# Fritzing sketch id0_skecx_0 (saved by Fritzing 0.9.3b)

parts:
  Часть1 = Arduino Leonardo (Rev3b)
  R1 = Resistor [tolerance=±5% resistance=220 package=THT]  # not connected
  R2 = Resistor [tolerance=±5% resistance=220 package=THT]
  R3 = Resistor [tolerance=±5% resistance=220 package=THT]  # not connected
  R4 = Resistor [tolerance=±5% resistance=220 package=THT]  # not connected
  R5 = Resistor [tolerance=±5% resistance=220 package=THT]  # not connected

nets:
  N1: Часть1.D2/SDA, R2.Pin_0

notes:
  сетевое питание 220-вольт
  USB-зарядка
  2-реле модуль
  реле 2
  ИК-приемник
  лампа
  насос
  реле 1
  датчик влажнсти почвы
  тонкие серые-сетевые провода
  толстые серые-проводазаремления
  желтые-логические
  красные-питание оборудование
  синие-управление реле
