# Fritzing sketch id1000_remote_car_alarm_attiny_0 (saved by Fritzing 0.9.2b)
circuit board: 1.94378cm x 3.19887cm
breadboards: 1

parts:
  ATTINY85 = attiny85 [package=dip]
  -BATT+ = Battery block 9V
  -BUZZ+ = Piezo Speaker
  REGULATOR_3_3V = LM1117DTX-3.3 
  C1 = Tantalum Capacitor [capacitance=10µF voltage=35V package="A 3216 [SMD, tantalum]"]
  C2 = Tantalum Capacitor [capacitance=10µF voltage=35V package="A 3216 [SMD, tantalum]"]
  D2 = Diode [package=sma-diode_alt]
  NRF24L1 = NRF24L01
  2N7000 = 2n7000 mosfet
  LED1 = LED - 5mm [color="Red (633nm)" package="5 mm [THT]"]
  R1 = Resistor [tolerance=±5% resistance=2.2k package=THT]

nets:
  N1: ATTINY85.Pin_2, NRF24L1.connector5, 2N7000.connector2
  N2: ATTINY85.Pin_3, NRF24L1.connector1
  N3: ATTINY85.Pin_4, -BATT+.-, REGULATOR_3_3V.connector0, C1.-, C2.-, NRF24L1.connector4, 2N7000.connector1
  N4: ATTINY85.Pin_5, NRF24L1.connector7
  N5: ATTINY85.Pin_6, NRF24L1.connector2
  N6: ATTINY85.Pin_7, NRF24L1.connector6
  N7: ATTINY85.Pin_8, REGULATOR_3_3V.connector1, REGULATOR_3_3V.connector3, C2.+, NRF24L1.connector0
  N8: -BATT+.+, -BUZZ+.pin2, D2.A, R1.Pin_1
  N9: -BUZZ+.pin1, 2N7000.connector0, LED1.cathode
  N10: REGULATOR_3_3V.connector2, C1.+, D2.C
  N11: LED1.anode, R1.Pin_0
