# Fritzing sketch id1001_car_beta1_0 (saved by Fritzing 0.8.7b)
breadboards: 1

parts:
  R1 = Resistor [tolerance=±10% resistance=220 package=THT]
  R2 = Resistor [tolerance=±5% resistance=220 package=THT]
  LED1 = smd LED [color="White (6500K)" package="1206 [SMD]"]
  LED2 = smd LED [color="White (6500K)" package="1206 [SMD]"]
  LED3 = smd LED [color="Yellow (592nm)" package="1206 [SMD]"]
  LED4 = smd LED [color="Yellow (592nm)" package="1206 [SMD]"]
  R3 = Resistor [tolerance=±10% resistance=220 package=THT]
  LED5 = smd LED [color="White (6500K)" package="1206 [SMD]"]
  R4 = Resistor [tolerance=±10% resistance=220 package=THT]
  R5 = Resistor [tolerance=±5% resistance=220 package=THT]
  LED6 = smd LED [color="White (6500K)" package="1206 [SMD]"]
  R6 = Resistor [tolerance=±10% resistance=220 package=THT]
  R7 = Resistor [tolerance=±10% resistance=220 package=THT]
  R8 = Resistor [tolerance=±10% resistance=220 package=THT]
  LED7 = LED - 5mm [color="Red (633nm)" package="5 mm [THT]"]
  LED8 = LED - 5mm [color="Red (633nm)" package="5 mm [THT]"]
  VCC1 = Battery
  K1 = Relay [part_number=FRS1B-S package=THT]  # not connected
  S1 = Toggle Switch [package=THT]

nets (from the breadboard view):
  N1: R1.Pin_0, LED1.anode
  N2: R1.Pin_1, R3.Pin_1, R4.Pin_1, R7.Pin_1, S1.L1
  N3: R2.Pin_0, LED1.cathode
  N4: R2.Pin_1, LED2.anode
  N5: LED2.cathode, LED4.cathode, LED6.cathode, LED8.cathode, VCC1.-
  N6: LED3.cathode, R6.Pin_1
  N7: LED3.anode, R3.Pin_0
  N8: LED4.anode, R6.Pin_0
  N9: LED5.cathode, R5.Pin_0
  N10: LED5.anode, R4.Pin_0
  N11: R5.Pin_1, LED6.anode
  N12: R7.Pin_0, LED7.anode
  N13: R8.Pin_0, LED8.anode
  N14: R8.Pin_1, LED7.cathode
  N15: VCC1.+, S1.COM
