# Fritzing sketch id1004_Bot_carton_alarma_0 (saved by Fritzing 0.9.3b)
breadboards: 1

parts:
  Componente1 = Arduino Uno (Rev3)
  R1 = Resistor [tolerance=±5% resistance=220 package=THT]
  R2 = Resistor [tolerance=±5% resistance=220 package=THT]
  J1 = Piezo Speaker
  hc-sr1 = hc-sr04
  LED1 = LED - 5mm [color="Red (633nm)" package="5 mm [THT]"]
  LED2 = LED - 5mm [color="Red (633nm)" package="5 mm [THT]"]

nets:
  N1: Componente1.D10_PWM/SS, hc-sr1.Echo
  N2: Componente1.D11_PWM/MOSI, hc-sr1.Trig
  N3: Componente1.D3_PWM, LED2.anode
  N4: Componente1.D4, LED1.anode
  N5: Componente1.D5_PWM, J1.pin2
  5V: Componente1.5V, hc-sr1.VCC
  GND: Componente1.GND, R1.Pin_0, R2.Pin_0, hc-sr1.GND
  N6: R1.Pin_1, LED2.cathode
  N7: R2.Pin_1, LED1.cathode

notes:
  Para la emisión de luz y sonido musical activado por diferentes distacias.
