# Fritzing sketch id1005_cardboardTV_remote_tx_0 (saved by Fritzing 0.9.2b)
circuit board: 6.74512cm x 5.05177cm

parts:
  Part3 = Arduino Nano (Rev3.0)
  U2 = RF-LINK_TX [package=rf-link_tx]
  S5 = SWITCH-MOMENTARY-2 [package=tactile-pth-12mm]
  S6 = SWITCH-MOMENTARY-2 [package=tactile-pth-12mm]
  S7 = SWITCH-MOMENTARY-2 [package=tactile-pth-12mm]
  S8 = SWITCH-MOMENTARY-2 [package=tactile-pth-12mm]
  BAT5 = BC9VPC [package=bc9vpc]  # not connected

nets:
  N1: Part3.D1/TX, U2.DATA
  GND: Part3.GND, U2.GND
  N2: Part3.D2, S5.2
  N3: Part3.D3, S6.2
  N4: Part3.D4, S8.2
  N5: Part3.D5, S7.2
  5V: Part3.5V, U2.+5V
  N6: S5.1, S7.1
