# Fritzing sketch id1006_Untitled_Sketch_2_0 (saved by Fritzing 0.9.3b)
breadboards: 1

parts:
  R1 = Resistor [tolerance=±5% resistance=220 package=THT]
  C1 = Electrolytic Capacitor [capacitance=1µF package="100 mil [THT, electrolytic]"]
  Componente1 = Arduino Uno (Rev3)

nets:
  N1: R1.Pin_0, Componente1.5V
  N2: R1.Pin_1, C1.-, Componente1.A0
  N3: C1.+, Componente1.GND
