# Fritzing sketch id1008_Untitled_Sketch_0 (saved by Fritzing 0.9.2b)
circuit board: 7.46948cm x 4.74132cm
breadboards: 1

parts:
  R1 = Resistor [tolerance=±5% resistance=220 package=THT]
  LED1 = LED - 5mm [color="Red (633nm)" package="5 mm [THT]"]
  IC1 = Voltage Regulator [package=to220-igo]
  VCC1 = Battery block 9V
  C2 = Electrolytic Capacitor [capacitance=10μF package="0605 [SMD, electrolytic]"]
  C3 = Electrolytic Capacitor [capacitance=10μF package="0605 [SMD, electrolytic]"]
  X1 = USB Connectors [package=usb-a-pcb]
  S1 = Toggle Switch [package=THT]

nets:
  N1: R1.Pin_0, LED1.cathode
  N2: R1.Pin_1, IC1.GND, VCC1.-, C2.-, C3.-, X1.VBUS
  N3: LED1.anode, IC1.OUT, C2.+, X1.GND
  N4: IC1.IN, C3.+, S1.COM
  N5: VCC1.+, S1.L1
