# Fritzing sketch id1009_carrera_de_pulsaciones_0 (saved by Fritzing 0.9.3b)
breadboards: 1

parts:
  Componente1 = Arduino Uno (Rev3)
  R1 = Resistor [tolerance=±5% resistance=220 package=THT]
  S1 = Momentary Switch [package=ksa_sealed_tac_switch]
  S2 = Momentary Switch [package=ksa_sealed_tac_switch]
  R2 = Resistor [tolerance=±5% resistance=220 package=THT]
  S3 = Momentary Switch [package=ksa_sealed_tac_switch]
  R3 = Resistor [tolerance=±5% resistance=220 package=THT]
  R4 = Resistor [tolerance=±5% resistance=220 package=THT]
  LED1 = LED - 5mm [color="Red (633nm)" package="5 mm [THT]"]
  LED2 = LED - 5mm [color="Green (570nm)" package="5 mm [THT]"]
  R5 = Resistor [tolerance=±5% resistance=220 package=THT]

nets:
  N1: Componente1.D8, R1.Pin_1, S1.4
  N2: Componente1.D9_PWM, S2.4, R2.Pin_1
  N3: Componente1.D10_PWM/SS, S3.4, R3.Pin_1
  N4: Componente1.D2, LED1.anode
  N5: Componente1.D3_PWM, LED2.anode
  N6: Componente1.5V, S1.2, S2.2, S3.2
  N7: Componente1.GND, R1.Pin_0, R2.Pin_0, R3.Pin_0, R4.Pin_0, R5.Pin_0
  N8: R4.Pin_1, LED1.cathode
  N9: LED2.cathode, R5.Pin_1

notes:
  CARRERA DE PULSACIONES
  ------------------------------------
  Se enciende el LED correspondiente al pulsador que alcance antes las 5 pulsaciones.
  Pin-8: Pulsador Verde
  Pin-9: Pulsador Rojo
  Pin-10: Reset a 0
