# Fritzing sketch id100_Arduino_1602_3_Wires_0 (saved by Fritzing 0.9.2b)
breadboards: 1

parts:
  Part1 = Arduino Uno (Rev3)
  LCD1 = LCD screen
  R1 = Rotary Potentiometer (Large) [maximum_resistance=100kΩ package=THT]
  U1 = 74HC595 [package="DIP16 [THT]"]
  Q1 = TRANSISTOR_NPN [package=to-92-ammo]
  Q2 = TRANSISTOR_NPN [package=to-92-ammo]  # not connected
  R4 = Rotary Potentiometer (Large) [maximum_resistance=100kΩ package=THT]  # not connected
  U2 = 74HC595 [package="DIP16 [THT]"]  # not connected
  LCD2 = LCD screen  # not connected

nets:
  N1: Part1.D9_PWM, U1.SH_CP
  N2: Part1.D7, U1.DS
  5V: Part1.5V, LCD1.VDD, LCD1.LED+, R1.leg1, U1.MR, U1.OE, U1.VCC
  GND: Part1.GND, LCD1.VSS, LCD1.R/W, R1.leg2, Q1.C
  N3: LCD1.V0, R1.wiper
  N4: LCD1.RS, U1.Q7
  N5: LCD1.E, U1.Q0
  N6: LCD1.DB4, U1.Q4
  N7: LCD1.DB5, U1.Q3
  N8: LCD1.DB6, U1.Q2
  N9: LCD1.DB7, U1.Q1
  N10: LCD1.LED-, U1.Q5, Q1.E
  N11: U1.Q6, Q1.B

notes:
  VSS
  VDD
  V0
  RS
  RW
  E
  D4
  D5
  D6
  D7
  A
  K
  EMITER
  BASE
  COLLECTOR
  ShiftReg pin 6
  ShiftReg pin 5
  GND
  PN 2222A
  10k Potentiometer
  V0 - LCD
  5V
  1602A LCD DISPLAY
  1
  2
  3
  4
  5
  6
  7
  8
  9
  10
  11
  12
  13
  14
  15
  16
  ShiftRegister
  D7 - LCD
  D6 - LCD
  RS - LCD
  Base - Transitor
  K - LCD & Emiter - Transistor
  D4 - LCD
  D5 - LCD
  5v
  LCD - E
  Pin 7 Arduino
  Pin 8 Arduino
  Pin 9 Arduino
  Do Not Connect
  ShiftReg Pin 5
  ShiftReg Pin 1
  ShiftReg Pin 2
  ShiftReg Pin 3
  ShiftReg Pin 4
  Middle Pin Potentiometer
  ShiftReg Pin 7
  ShiftReg Pin 15
  ARDUINO UNO
  Author: Sergio Fernandez
