# Fritzing sketch id1010_carro_bluetooh_0 (saved by Fritzing 0.9.3b)
breadboards: 1

parts:
  Parte1 = Arduino Uno (Rev3)
  IC1 = L293D [package=THT]
  M1 = DC Motor
  M2 = DC Motor
  Parte2 = HC-SR04 ultrasonic distance sensor
  Parte3 = bluetooth-module
  VCC1 = Battery

nets:
  N1: Parte1.D9_PWM, IC1.In_2
  N2: Parte1.D10_PWM/SS, IC1.In_1
  N3: Parte1.D0/RX, Parte3.connector15
  N4: Parte1.D1/TX, Parte3.connector16
  N5: Parte1.D2, Parte2.connector2
  N6: Parte1.D3_PWM, Parte1.5V, IC1.Enable_1, IC1.Enable_2, IC1.+V, Parte2.connector0, Parte2.connector1, Parte3.connector13
  N7: Parte1.D5_PWM, IC1.In_3
  N8: Parte1.D6_PWM, IC1.In_4
  N9: Parte1.GND, IC1.0V, IC1.+Vmotor, Parte2.connector3, Parte3.connector14, VCC1.connector0, VCC1.connector1
  N10: IC1.Out_1_(_Controlled_by_Enable_1_), M1.pin_2
  N11: IC1.Out_2_(_Controlled_by_Enable_1_), M1.pin_1
  N12: IC1.Out_3_(_Controlled_by_Enable_2_), M2.pin_2
  N13: IC1.Out_4_(_Controlled_by_Enable_2_), M2.pin_1
