# Fritzing sketch id1011_Untitled_Sketch_4_0 (saved by Fritzing 0.9.0b)
breadboards: 1

parts:
  Componente1 = Arduino Uno (Rev3)
  M1 = DC Motor
  M2 = DC Motor
  BAT1 = BC9VPC [package=bc9vpc]
  Componente2 = Bluetooth Mate Silver
  IC1 = L293D [package=THT]
  R1 = Resistor [tolerance=±5% resistance=220 package="0805 [SMD]"]
  R2 = Resistor [package="2010 [SMD]"]
  LED1 = LEDs [package=led10mm]
  LED2 = LEDs [package=led10mm]
  LED3 = LEDs [package=led10mm]  # not connected
  LED4 = LEDs [package=led10mm]  # not connected

nets:
  N1: Componente1.A0, R1.Pin_1, R2.Pin_0
  N2: Componente1.D9_PWM, IC1.In_1
  N3: Componente1.GND, BAT1.V+, Componente2.TX_5V, R2.Pin_1
  N4: Componente1.D0/RX, Componente2.VCC
  N5: Componente1.D1/TX, Componente2.CTS_5V
  N6: Componente1.D2, Componente2.GND
  N7: Componente1.D5_PWM, IC1.In_4
  N8: Componente1.D6_PWM, IC1.In_3
  N9: Componente1.5V, Componente2.RX_5V, IC1.Enable_1, IC1.Enable_2, IC1.+V
  N10: Componente1.VIN, BAT1.V-
  N11: M1.pin_1, IC1.Out_4_(_Controlled_by_Enable_2_)
  N12: M1.pin_2, IC1.Out_3_(_Controlled_by_Enable_2_)
  N13: M2.pin_1, IC1.Out_2_(_Controlled_by_Enable_1_)
  N14: M2.pin_2, IC1.Out_1_(_Controlled_by_Enable_1_)
  N15: IC1.+Vmotor, R1.Pin_0
  N16: LED1.A, LED2.A
  N17: LED1.C, LED2.C
