# Fritzing sketch id1012_hardware_0 (saved by Fritzing 0.8.5b)
breadboards: 1

parts:
  U1 = TLP621 [package=THT]
  U2 = TLP621 [package=THT]
  U3 = TLP621 [package=THT]
  U4 = TLP621 [package=THT]
  LED1 = LED - 5mm [color="Red (633nm)" package="5 mm [THT]"]
  LED2 = LED - 5mm [color="Red (633nm)" package="5 mm [THT]"]
  T1 = LM34 Temperature Sensor [package="TO92 [THT]"]
  S1 = Pushbutton [package="[THT]"]
  S2 = Pushbutton [package="[THT]"]
  S3 = Pushbutton [package="[THT]"]
  S4 = Pushbutton [package="[THT]"]
  Part1 = Arduino Uno (Rev3)

nets:
  N1: U1.Pin_1, Part1.D3_PWM
  N2: U1.Pin_2, U2.Pin_2, U3.Pin_2, U4.Pin_2, LED1.cathode, LED2.cathode, T1.GND
  N3: U1.Pin_4, S3.Pin_1, S3.Pin_2
  N4: U1.Pin_3, S3.Pin_3, S3.Pin_4
  N5: U2.Pin_1, Part1.D2
  N6: U2.Pin_4, S2.Pin_4
  N7: U2.Pin_3, S2.Pin_2
  N8: U3.Pin_1, Part1.D1/TX
  N9: U3.Pin_4, S1.Pin_1, S1.Pin_2
  N10: U3.Pin_3, S1.Pin_3, S1.Pin_4
  N11: U4.Pin_1, Part1.D0/RX
  N12: U4.Pin_4, S4.Pin_1, S4.Pin_2
  N13: U4.Pin_3, S4.Pin_3, S4.Pin_4
  N14: LED1.anode, Part1.D4
  N15: LED2.anode, Part1.D5_PWM
  N16: T1.+Vs, Part1.3V3
  N17: T1.Vout, Part1.A0

notes:
  start
  lock
  unlock
  trunk
  Imagine this is a Spark Core. All connected pins are the same and the Core sits in the breadboard perfectly.
