# Fritzing sketch id1013_temperature_sensor_msJox7Ivs8_1_0 (saved by Fritzing 0.9.3b)
circuit board: 7.36494cm x 7.90305cm
breadboards: 1

parts:
  R2 = Rotary Potentiometer (Small) [maximum_resistance=100kΩ package=THT]
  LCD2 = LCD screen
  T3 = LM35 Temperature Sensor [package="TO92 [THT]"]
  R3 = Resistor [tolerance=±5% resistance=220 package=THT]
  Part2 = Arduino Uno (Rev3)

nets (from the schematic view):
  VDD: R2.leg1, LCD2.VDD, T3.+Vs, R3.Pin_0, Part2.5V
  N1: R2.wiper, LCD2.V0
  GND: R2.leg2, LCD2.VSS, LCD2.R/W, LCD2.LED-, T3.GND, Part2.GND
  N2: LCD2.RS, Part2.D12/MISO
  N3: LCD2.E, Part2.D11_PWM/MOSI
  N4: LCD2.DB4, Part2.D2
  N5: LCD2.DB5, Part2.D3_PWM
  N6: LCD2.DB6, Part2.D4
  N7: LCD2.DB7, Part2.D5_PWM
  N8: LCD2.LED+, R3.Pin_1
  N9: T3.Vout, Part2.A0
