# Fritzing sketch id1015_casomerilec_0 (saved by Fritzing 0.9.3b)
breadboards: 1

parts:
  LCD1 = LCD screen
  Part1 = Arduino Uno (Rev3)
  Part2 = Bluetooth HC-05 Macho
  hc-sr1 = hc-sr04
  R1 = Trimmer Potentiometer [maximum_resistance=10kΩ package=THT]
  R2 = Resistor [tolerance=±5% resistance=220 package=THT]
  R3 = Resistor [tolerance=±5% resistance=1k package=THT]
  R4 = Resistor [tolerance=±5% resistance=2.2k package=THT]
  LED1 = LED - 5mm [color="Red (633nm)" package="5 mm [THT]"]
  LED2 = LED - 5mm [color="Yellow (595nm)" package="5 mm [THT]"]
  LED3 = LED - 5mm [color="Green (565nm)" package="5 mm [THT]"]
  R5 = Resistor [tolerance=±5% resistance=220 package=THT]
  R6 = Resistor [tolerance=±5% resistance=220 package=THT]
  R7 = Resistor [tolerance=±5% resistance=220 package=THT]

nets:
  GND: LCD1.VSS, LCD1.R/W, LCD1.LED-, Part1.GND, Part2.GND, hc-sr1.GND, R1.leg1, R4.Pin_0, R5.Pin_0, R6.Pin_0, R7.Pin_0
  VDD: LCD1.VDD, Part1.5V, hc-sr1.VCC, R1.leg2, R2.Pin_0
  N1: LCD1.V0, R1.wiper
  N2: LCD1.RS, Part1.D12/MISO
  N3: LCD1.E, Part1.D11_PWM/MOSI
  N4: LCD1.DB4, Part1.D5_PWM
  N5: LCD1.DB5, Part1.D4
  N6: LCD1.DB6, Part1.D3_PWM
  N7: LCD1.DB7, Part1.D2
  N8: LCD1.LED+, R2.Pin_1
  N9: Part1.D8, LED1.anode
  N10: Part1.D9_PWM, hc-sr1.Trig
  N11: Part1.D10_PWM/SS, LED3.anode
  N12: Part1.D13/SCK, hc-sr1.Echo
  N13: Part1.D0/RX, Part2.RXD
  N14: Part1.D1/TX, R3.Pin_1
  N15: Part1.D6_PWM, LED2.anode
  3V3: Part1.3V3, Part2.VCC
  N16: R3.Pin_0, R4.Pin_1
  N17: LED1.cathode, R7.Pin_1
  N18: LED2.cathode, R6.Pin_1
  N19: LED3.cathode, R5.Pin_1
