# Fritzing sketch id1016_Progetto_Telecomunicazioni_0 (saved by Fritzing 0.9.3b)
breadboards: 1

parts:
  Componente1 = Arduino Uno (Rev3)
  R1 = Resistor [tolerance=±5% resistance=220 package=THT]
  LED1 = LED - 5mm [color="Red (633nm)" package="5 mm [THT]"]
  LED2 = LED - 5mm [color="Green (555nm)" package="5 mm [THT]"]
  R2 = Resistor [tolerance=±5% resistance=220 package=THT]
  1 = Pushbutton [package="[THT]"]
  2 = Pushbutton [package="[THT]"]
  3 = Pushbutton [package="[THT]"]
  4 = Pushbutton [package="[THT]"]
  Reimposta_Combinazione = Pushbutton [package="[THT]"]
  R3 = Resistor [tolerance=±5% resistance=220 package=THT]
  R4 = Resistor [tolerance=±5% resistance=220 package=THT]
  R5 = Resistor [tolerance=±5% resistance=220 package=THT]
  R6 = Resistor [tolerance=±5% resistance=220 package=THT]
  R7 = Resistor [tolerance=±5% resistance=220 package=THT]
  Sblocco = Pushbutton [package="[THT]"]
  R8 = Resistor [tolerance=±5% resistance=220 package=THT]
  Chiudi_Cassaforte = Pushbutton [package="[THT]"]
  R9 = Resistor [tolerance=±5% resistance=220 package=THT]
  LED3 = LED - 5mm [color="Yellow (574nm)" package="5 mm [THT]"]
  R10 = Resistor [tolerance=±5% resistance=220 package=THT]
  R11 = Resistor [tolerance=±5% resistance=220 package=THT]
  LED4 = LED - 5mm [color="Orange (620nm)" package="5 mm [THT]"]

nets:
  N1: Componente1.D8, Chiudi_Cassaforte.Pin_1, Chiudi_Cassaforte.Pin_2, R9.Pin_0
  N2: Componente1.D10_PWM/SS, R11.Pin_0
  N3: Componente1.D11_PWM/MOSI, R10.Pin_0
  N4: Componente1.D12/MISO, R2.Pin_0
  N5: Componente1.D13/SCK, R1.Pin_0
  N6: Componente1.GND, LED1.anode, LED2.anode, R3.Pin_1, R4.Pin_1, R5.Pin_1, R6.Pin_1, R7.Pin_1, R8.Pin_1, R9.Pin_1, LED3.anode, LED4.anode
  N7: Componente1.D2, Sblocco.Pin_1, Sblocco.Pin_2, R8.Pin_0
  N8: Componente1.D3_PWM, Reimposta_Combinazione.Pin_1, Reimposta_Combinazione.Pin_2, R5.Pin_0
  N9: Componente1.D4, 4.Pin_1, 4.Pin_2, R7.Pin_0
  N10: Componente1.D5_PWM, 3.Pin_1, 3.Pin_2, R6.Pin_0
  N11: Componente1.D6_PWM, 2.Pin_1, 2.Pin_2, R4.Pin_0
  N12: Componente1.D7, 1.Pin_1, 1.Pin_2, R3.Pin_0
  N13: Componente1.5V, 1.Pin_3, 1.Pin_4, 2.Pin_3, 2.Pin_4, 3.Pin_3, 3.Pin_4, 4.Pin_3, 4.Pin_4, Reimposta_Combinazione.Pin_3, Reimposta_Combinazione.Pin_4, Sblocco.Pin_3, Sblocco.Pin_4, Chiudi_Cassaforte.Pin_3, Chiudi_Cassaforte.Pin_4
  N14: R1.Pin_1, LED1.cathode
  N15: LED2.cathode, R2.Pin_1
  N16: LED3.cathode, R10.Pin_1
  N17: R11.Pin_1, LED4.cathode
