# Fritzing sketch id1017_cat_fancy_0 (saved by Fritzing 0.9.1b)
breadboards: 1

parts:
  LCD1 = LCD screen
  Part1 = Arduino Uno (Rev3)
  R1 = Rotary Potentiometer (Small) [maximum_resistance=100kΩ package=THT]
  Q1 = NPN-Transistor [package="TO92 [THT]"]
  J1 = Basic Servo
  J2 = Basic Servo

nets:
  VSS: LCD1.VSS, LCD1.R/W, LCD1.LED-, Part1.GND, R1.leg2, Q1.C
  VCC: LCD1.VDD, LCD1.LED+, Part1.5V, R1.leg1, J1.vcc, J2.vcc
  N1: LCD1.V0, R1.wiper
  N2: LCD1.RS, Part1.D12/MISO
  N3: LCD1.E, Part1.D11_PWM/MOSI
  N4: LCD1.DB4, Part1.D5_PWM
  N5: LCD1.DB5, Part1.D4
  N6: LCD1.DB6, Part1.D3_PWM
  N7: LCD1.DB7, Part1.D2
  N8: Part1.D8, Q1.B
  N9: Part1.D9_PWM, J1.pulse
  N10: Part1.D10_PWM/SS, J2.pulse
  GND: Q1.E, J1.gnd, J2.gnd
