# Fritzing sketch id1019_Sketch_Catamarano_0 (saved by Fritzing 0.8.7b)
breadboards: 1

parts:
  J1 = Basic Servo
  Q1 = Basic FET N-Channel [package="TO220 [THT]"]
  D1 = Rectifier Diode [part_number=1N4001 package="300 mil [THT]"]
  LED1 = LED - 5mm [color="Red (633nm)" package="5 mm [THT]"]
  T1 = LM35 Temperature Sensor [package="TO92 [THT]"]
  FAN = DC Motor
  Battery_12V = Battery
  Componente1 = Arduino Uno (Rev3) - ICSP

nets:
  GND: J1.gnd, Q1.source, D1.anode, LED1.cathode, T1.GND, Battery_12V.+, Componente1.GND
  VCC: J1.vcc, T1.+Vs, Componente1.5V
  N1: J1.pulse, Componente1.D8
  N2: Q1.gate, FAN.pin_2, Componente1.D5_PWM
  N3: Q1.drain, D1.cathode, Battery_12V.-
  N4: LED1.anode, Componente1.ICSP_SCK, Componente1.D13/SCK
  N5: T1.Vout, Componente1.A0
  N6: FAN.pin_1, Componente1.VIN

notes:
  <--- Ventola
  <-- 2 Batterie da 6v l'una (12v totali)
  Controllare bene positivo e negativo batterie 12v (Vedere immagine Mosfet+battery in cartella "Arduino")
