# Fritzing sketch id1021_caterpillar_0 (saved by Fritzing 0.9.2b)
breadboards: 1

parts:
  Composant1 = Arduino Uno (Rev3)
  LED1 = LED - 5mm [color="Red (633nm)" package="5 mm [THT]"]
  LED2 = LED - 5mm [color="Yellow (592nm)" package="5 mm [THT]"]
  LED3 = LED - 5mm [color="Green (565nm)" package="5 mm [THT]"]
  LED4 = LED - 5mm [color="Blue (470nm)" package="5 mm [THT]"]
  R1 = Resistor [tolerance=±5% resistance=220 package=THT]
  R2 = Resistor [tolerance=±5% resistance=220 package=THT]
  R3 = Resistor [tolerance=±5% resistance=220 package=THT]
  R4 = Resistor [tolerance=±5% resistance=220 package=THT]

nets:
  N1: Composant1.D8, LED1.cathode
  N2: Composant1.D9_PWM, LED2.cathode
  N3: Composant1.D10_PWM/SS, LED3.cathode
  N4: Composant1.D11_PWM/MOSI, LED4.cathode
  N5: Composant1.5V, R1.Pin_0, R2.Pin_0, R3.Pin_0, R4.Pin_0
  N6: LED1.anode, R1.Pin_1
  N7: LED2.anode, R2.Pin_1
  N8: LED3.anode, R3.Pin_1
  N9: LED4.anode, R4.Pin_1
