# Fritzing sketch id1022_Raspberry_Pi_Real_Time_1_0 (saved by Fritzing 0.8.7b)
breadboards: 1

parts:
  Raspberry_Pi_B_rev2 = Raspberry Pi B rev2
  LED1 = LED - 5mm [color="Red (633nm)" package="5 mm [THT]"]
  R3 = Resistor [tolerance=±5% resistance=1k package=THT]
  S1 = Pushbutton [package="[THT]"]
  R5 = Resistor [tolerance=±5% resistance=1k package=THT]

nets:
  N1: Raspberry_Pi_B_rev2.5V, S1.Pin_3, S1.Pin_4
  N2: Raspberry_Pi_B_rev2.GND, LED1.cathode, R5.Pin_1
  N3: Raspberry_Pi_B_rev2.GPIO_10, S1.Pin_1, S1.Pin_2, R5.Pin_0
  N4: Raspberry_Pi_B_rev2.GPIO_11, R3.Pin_0
  N5: LED1.anode, R3.Pin_1
