# Fritzing sketch id1025_BNO055_0 (saved by Fritzing 0.9.3b)
circuit board: 10cm x 6cm
breadboards: 1

parts:
  Componente1 = BNO055
  Componente2 = Arduino Mega 2560 (Rev3)

nets:
  N1: Componente1.connector17, Componente2.3V3
  N2: Componente1.connector18, Componente2.GND
  N3: Componente1.connector19, Componente2.D20/SDA, Componente2.SDA
  N4: Componente1.connector20, Componente2.D21/SCL
  N5: Componente1.connector24, Componente2.D2_PWM

notes:
  [BNO055
