# Fritzing sketch id1026_cctalk_rev3_0 (saved by Fritzing 0.9.0b)
circuit board: 4.38967cm x 3.02189cm
breadboards: 1

parts:
  R1 = Resistor [tolerance=±5% resistance=68k package=THT]
  R2 = Resistor [tolerance=±5% resistance=100k package=THT]
  TTL = female pin header, 4 pins [form="♀ (female)"]
  Q1 = PNP-Transistor [package="TO92 [THT]"]
  R3 = Resistor [tolerance=±5% resistance=68k package=THT]
  R4 = Resistor [tolerance=±5% resistance=100k package=THT]
  R5 = Resistor [tolerance=±5% resistance=100k package=THT]
  D1 = Schottky Diode [part_number=1N5817 package="300 mil [THT]"]
  Q2 = NPN-Transistor [package="TO92 [THT]"]
  R6 = Resistor [tolerance=±5% resistance=47 package=THT]
  cctalk = shrouded pin header, 10 pins [form="♂ (shrouded male)"]
  R7 = Resistor [tolerance=±5% resistance=10k package=THT]
  J1 = Screw terminal - 2 pins [package=THT]

nets:
  N1: R1.Pin_0, R2.Pin_0, Q1.B
  TX: R1.Pin_1, TTL.pin2
  +5V: R2.Pin_1, TTL.pin3, Q1.E, R4.Pin_1, R7.Pin_1
  GND: TTL.pin1, R5.Pin_0, Q2.E
  RX: TTL.pin4, R4.Pin_0, D1.anode
  N2: Q1.C, R3.Pin_1
  N3: R3.Pin_0, R5.Pin_1, Q2.B
  CCtalk Data: D1.cathode, R6.Pin_0, cctalk.pin1, R7.Pin_0
  N4: Q2.C, R6.Pin_1
  CCtalk_GND: cctalk.pin4, cctalk.pin8, J1.pin2
  CCtalk +V: cctalk.pin7, cctalk.pin10, J1.pin1
