# Fritzing sketch id1028_CD_4069_finger_drum_0 (saved by Fritzing 0.9.2b)
circuit board: 8.38044cm x 7.95546cm
breadboards: 1

parts:
  4069_cn = IC, DIP package, 14 pins [chip_label=IC]
  +9-12V = Battery
  Dual_20k_pot_CUTOFF = POT [package=pot_alpha_rv16af-20]
  U2 = POT [package=pot_alpha_rv16af-20]
  audio_in = Pad [width=2.39889411111112 height=2.257784 connect=center]
  0_1Uf = Tantalum Capacitor [capacitance=1μF package="100 mil [THT, tantalum]"]
  0_1Uf_2 = Tantalum Capacitor [capacitance=1μF package="100 mil [THT, tantalum]"]
  6_8K = Resistor [tolerance=±5% resistance=220 package=THT]
  100K_POt_RES = POT [package=pot_alpha_rv16af-20]
  10K = Resistor [tolerance=±5% resistance=220 package=THT]
  10K_2 = Resistor [tolerance=±5% resistance=220 package=THT]
  out2 = Pad [width=3.47350965943361 height=3.73402332149788 connect=center]
  out = Pad [width=3.47350965943361 height=3.73402332149788 connect=center]
  optional_1Uf_output_cap = Pad [width=2.93511495111173 height=2.70933802666741 connect=center]  # not connected
  npn = NPN-Transistor [package="TO92 [THT]"]
  piezo_disc = Microphone

nets:
  N1: 4069_cn.pin1, 6_8K.Pin_0, 10K.Pin_0, 10K_2.Pin_0
  N2: 4069_cn.pin2, U2.A, 10K_2.Pin_1
  N3: 4069_cn.pin3, U2.S, U2.E, 0_1Uf.-
  N4: 4069_cn.pin4, Dual_20k_pot_CUTOFF.A, 0_1Uf.+, out2.pad
  N5: 4069_cn.pin5, 0_1Uf_2.-
  N6: 4069_cn.pin6, 0_1Uf_2.+, 100K_POt_RES.S, 100K_POt_RES.E, out.pad
  N7: 4069_cn.pin7, 4069_cn.pin9, 4069_cn.pin11, 4069_cn.pin13, +9-12V.+, piezo_disc.pin2
  N8: 4069_cn.pin14, +9-12V.-
  N9: Dual_20k_pot_CUTOFF.S, Dual_20k_pot_CUTOFF.E
  N10: audio_in.pad, 10K.Pin_1, npn.E
  N11: 6_8K.Pin_1, 100K_POt_RES.A
  N12: npn.B, piezo_disc.pin1

notes:
  cd4069 drum generator with piezo for finger drumming
  0V
