# Fritzing sketch id1029_cdi_1_0 (saved by Fritzing 0.7.10b)
perfboards: 1

parts:
  R2 = Resistor [tolerance=±5% resistance=68k package=THT]
  D2 = Rectifier Diode [part_number=1N4001 package="300 mil [THT]"]
  D3 = Rectifier Diode [part_number=1N4001 package="300 mil [THT]"]
  Q1 = NPN-Transistor [package="TO92 [THT]"]
  R3 = Resistor [tolerance=±5% resistance=220 package=THT]
  C2 = Electrolytic Capacitor [capacitance="1 μF" package="300 mil [THT, electrolytic]"]
  R4 = Resistor [tolerance=±5% resistance=220 package=THT]
  C3 = Ceramic Capacitor [capacitance=100nF voltage=10V package="100 mil [THT, multilayer]"]
  Pad1 = Pad [width=7.90222222222222 height=9.03111111111111 connect=center]  # not connected

nets (from the schematic view):
  N1: R2.Pin_0, D2.anode
  N2: D2.cathode, Q1.C, C2.+
  N3: D3.cathode, Q1.E, R3.Pin_1
  N4: Q1.B, R4.Pin_0
  N5: R4.Pin_1, C3.1
