# Fritzing sketch id102_3v_to_5v_0 (saved by Fritzing 0.8.3b)
breadboards: 1

parts:
  IC1 = IC, DIP package, 8 pins [chip_label=IC]
  L1 = Inductor [inductance=22µH package="400 mil [THT]"]
  D1 = Rectifier Diode [part_number=1N5817 package="300 mil [THT]"]
  C1 = Electrolytic Capacitor [capacitance=100µF package="100 mil [THT, electrolytic]"]
  C2 = Electrolytic Capacitor [capacitance=100µF package="100 mil [THT, electrolytic]"]
  C3 = Ceramic Capacitor [capacitance=1µF package="100 mil [THT, multilayer]"]
  C4 = Ceramic Capacitor [capacitance=1µF package="100 mil [THT, multilayer]"]
  VCC1 = Battery

nets:
  N1: IC1.pin1, L1.pin_0, C1.+, VCC1.+
  N2: IC1.pin2, IC1.pin7, C1.-, C2.-, C3.1, C4.0, VCC1.-
  N3: IC1.pin3, C3.0
  N4: IC1.pin8, L1.pin_1, D1.anode
  N5: D1.cathode, C2.+, C4.1

notes:
  MAXIM 756
  output +
  output -
