# Fritzing sketch id1032_cds_0 (saved by Fritzing 0.9.3b)
breadboards: 1

parts:
  パーツ1 = Arduino Leonardo (Rev3b)
  R1 = Resistor [tolerance=±5% resistance=10 package=THT]
  R2 = PHOTOCELL [package=photocell-kit]

nets:
  N1: パーツ1.5V, R2.P$2
  N2: パーツ1.GND, R1.Pin_0
  N3: パーツ1.A0, R1.Pin_1, R2.P$1

notes:
  10kΩ
