# Fritzing sketch id1033_CDS_LEDs2_0 (saved by Fritzing 0.9.0b)
breadboards: 1

parts:
  パーツ1 = Arduino Nano (Rev3.0)
  R5 = Resistor [tolerance=±5% resistance=1k package=THT]
  R2 = Resistor [tolerance=±5% resistance=1k package=THT]
  R3 = Resistor [tolerance=±5% resistance=1k package=THT]
  LED1 = LED - 5mm [color="Red (633nm)" package="5 mm [THT]"]
  LED2 = LED - 5mm [color="Green (570nm)" package="5 mm [THT]"]
  LED3 = LED - 5mm [color="Blue (525nm)" package="5 mm [THT]"]
  R4 = PHOTOCELL [package=photocell]

nets:
  N1: パーツ1.GND, LED1.cathode, LED2.cathode, LED3.cathode, R4.P$1
  N2: パーツ1.D10, R3.Pin_0
  N3: パーツ1.D11/MOSI, R2.Pin_0
  N4: パーツ1.D12/MISO, R5.Pin_0
  N5: パーツ1.A0, R4.P$2
  N6: R5.Pin_1, LED1.anode
  N7: R2.Pin_1, LED2.anode
  N8: R3.Pin_1, LED3.anode

notes:
  明るさに応じてLEDの点滅速度が変わります。
