# Fritzing sketch id1034_CDS+LEDs_0 (saved by Fritzing 0.9.0b)
circuit board: 6.88566cm x 5.36311cm
circuit board: 6.88566cm x 5.36311cm
breadboards: 1

parts:
  Arduino_UNO = Arduino Uno (Rev3)
  R1 = Resistor [tolerance=±5% resistance=1k package=THT]
  R2 = Resistor [tolerance=±5% resistance=1k package=THT]
  R3 = Resistor [tolerance=±5% resistance=1k package=THT]
  LED1 = LED - 5mm [color="Red (633nm)" package="5 mm [THT]"]
  LED2 = LED - 5mm [color="Green (570nm)" package="5 mm [THT]"]
  LED3 = LED - 5mm [color="Blue (525nm)" package="5 mm [THT]"]
  R4 = PHOTOCELL [package=photocell]

nets:
  N1: Arduino_UNO.A0, R4.P$2
  N2: Arduino_UNO.GND, LED1.cathode, LED2.cathode, LED3.cathode, R4.P$1
  N3: Arduino_UNO.D3_PWM, R1.Pin_0
  N4: Arduino_UNO.D5_PWM, R2.Pin_0
  N5: Arduino_UNO.D6_PWM, R3.Pin_0
  N6: R1.Pin_1, LED1.anode
  N7: R2.Pin_1, LED2.anode
  N8: R3.Pin_1, LED3.anode

notes:
  光の強さに応じて、RGBのLEDが3桁の2進数としてカウントアップする速度が変化します。
