# Fritzing sketch id1035_us_multipe_V3_0 (saved by Fritzing 0.9.3b)
perfboards: 1

parts:
  hc-sr1 = hc-sr04  # not connected
  Composant2 = Arduino Nano (Rev3.0)
  J19 = female pin header, 4 pins [form="♀ (female)"]  # not connected
  J20 = female pin header, 4 pins [form="♀ (female)"]
  J21 = female pin header, 4 pins [form="♀ (female)"]
  J22 = female pin header, 4 pins [form="♀ (female)"]
  J23 = female pin header, 4 pins [form="♀ (female)"]
  J24 = male pin header, 4 pins [form="♂ (male)"]  # not connected
  J25 = male pin header, 4 pins [form="♂ (male)"]
  J26 = male pin header, 4 pins [form="♂ (male)"]
  J27 = female pin header, 4 pins [form="♀ (female)"]

nets:
  N1: Composant2.5V, J20.pin4
  N2: J21.pin4, J25.pin4
  N3: J22.pin4, J25.pin1, J27.pin1
  N4: J23.pin1, J26.pin1
