# Fritzing sketch id1036_us_multipe_V4_0 (saved by Fritzing 0.9.3b)
perfboards: 1

parts:
  hc-sr1 = hc-sr04  # not connected
  Composant2 = Arduino Nano (Rev3.0)
  J4 = female pin header, 4 pins [form="♀ (female)"]  # not connected
  J6 = female pin header, 4 pins [form="♀ (female)"]  # not connected
  J9 = male pin header, 4 pins [form="♂ (male)"]
  J10 = male pin header, 4 pins [form="♂ (male)"]
  J11 = male pin header, 4 pins [form="♂ (male)"]
  J12 = female pin header, 4 pins [form="♀ (female)"]  # not connected
  J14 = female pin header, 4 pins [form="♀ (female)"]  # not connected
  J15 = female pin header, 4 pins [form="♀ (female)"]
  J16 = female pin header, 4 pins [form="♀ (female)"]
  J17 = female pin header, 4 pins [form="♀ (female)"]
  J18 = female pin header, 4 pins [form="♀ (female)"]
  J19 = female pin header, 4 pins [form="♀ (female)"]
  J20 = female pin header, 4 pins [form="♀ (female)"]

nets:
  N1: Composant2.D2, J10.pin3
  N2: Composant2.D3, J10.pin2
  N3: Composant2.D4, J15.pin3
  N4: Composant2.D5, J15.pin2
  N5: Composant2.D6, J16.pin3
  N6: Composant2.D7, J16.pin2
  N7: Composant2.D8, J20.pin3
  N8: Composant2.D9, J20.pin2
  N9: Composant2.D10, J18.pin3
  N10: Composant2.D11/MOSI, J18.pin2
  N11: Composant2.D12/MISO, J9.pin2
  N12: Composant2.A5, J11.pin3
  N13: Composant2.A4, J11.pin2
  N14: Composant2.A3, J17.pin2
  N15: Composant2.A2, J17.pin3
  N16: Composant2.A1, J19.pin3
  N17: Composant2.A0, J19.pin2
