# Fritzing sketch id1037_headset_0 (saved by Fritzing 0.3.19b)

parts:
  Arduino1 = Arduino
  LED1 = Red LED - 5mm
  Q1 = NPN-Transistor [package="TO92 [THT]"]
  R1 = Resistor [resistance=220 package=THT]
  D1 = Zener Diode [package="300 mil [THT]"]

nets:
  GND: Arduino1.GND, Q1.C, R1.Pin_0
  N1: Arduino1.D13, LED1.anode
  N2: Arduino1.D12, D1.cathode
  N3: LED1.cathode, R1.Pin_1
  N4: Q1.B, D1.anode

notes:
  Q1 emitter is connected to cellphone microphone line, which carries -2.5 V
  NPN emitter is connected to cellphone microphone line, which carries -2.5 V
  NPN collector is grounded to Arduino and cellphone
  Q1 collector is grounded to Arduino and cellphone
