# Fritzing sketch id1038_Cellucon.Arduino_0 (saved by Fritzing 0.9.3b)
perfboards: 2

parts:
  Arduino_Pro_Mini = Arduino Pro Mini v13
  RC-Rudder = Basic Servo
  Motor_Power_(ESC) = Basic Servo
  Camera-Tilt = Basic Servo
  Camera-Pan = Basic Servo
  US1881 = IC, SIP package, 3 pins [chip_label=IC]
  J4 = Dagu DGServo 9g header (male) [package=THT]
  S4 = Dagu DGServo 9g header connector (female) [package=THT]
  J3 = Dagu DGServo 9g header (male) [package=THT]
  J2 = Dagu DGServo 9g header (male) [package=THT]
  J1 = Dagu DGServo 9g header (male) [package=THT]
  S3 = Dagu DGServo 9g header connector (female) [package=THT]
  S2 = Dagu DGServo 9g header connector (female) [package=THT]
  S1 = Dagu DGServo 9g header connector (female) [package=THT]
  R3 = Resistor [tolerance=±1% resistance=1.5k package=THT]
  R2 = Resistor [tolerance=±1% resistance=1.5k package=THT]
  バッテリ電圧 = female pin header, 2 pins [form="♀ (female)"]
  RN42 = Bluetooth Module Breakout - Roving Networks (RN-41)  # not connected
  R1 = Resistor [tolerance=±5% resistance=10k package=THT]
  LP2950L-3_3V = Voltage Regulator - 3.3V [package="TO220 [THT]"]
  C1 = Electrolytic Capacitor [capacitance=47µF voltage=10V package="100 mil [THT, electrolytic]"]  # not connected
  C2 = Ceramic Capacitor [capacitance=100nF voltage=50V package="100 mil [THT, multilayer]"]
  R6 = Resistor [tolerance=±5% resistance=3.3k package=THT]  # not connected
  R7 = Resistor [tolerance=±5% resistance=2.2k package=THT]  # not connected

nets (from the breadboard view):
  VCC: Arduino_Pro_Mini.VCC, US1881.pin1, J4.Vcc, J3.Vcc, J2.Vcc, J1.Vcc, R1.Pin_0, LP2950L-3_3V.input_voltage, C2.0
  GND: Arduino_Pro_Mini.GND, US1881.pin2, J4.gnd, J3.gnd, J2.gnd, J1.gnd, R3.Pin_1, バッテリ電圧.pin1, LP2950L-3_3V.GND, C2.1
  N1: Arduino_Pro_Mini.A0, R3.Pin_0, R2.Pin_1
  N2: Arduino_Pro_Mini.D10_PWM/SS, J1.pulse
  N3: Arduino_Pro_Mini.D9_PWM, J2.pulse
  N4: Arduino_Pro_Mini.D6_PWM, J3.pulse
  N5: Arduino_Pro_Mini.D5_PWM, J4.pulse
  N6: Arduino_Pro_Mini.D2, US1881.pin3, R1.Pin_1
  GND_2: RC-Rudder.gnd, S2.gnd
  VCC_2: RC-Rudder.vcc, S2.Vcc
  N7: RC-Rudder.pulse, S2.pulse
  GND_3: Motor_Power_(ESC).gnd, S1.gnd
  VCC_3: Motor_Power_(ESC).vcc, S1.Vcc
  N8: Motor_Power_(ESC).pulse, S1.pulse
  GND_4: Camera-Tilt.gnd, S3.gnd
  VCC_4: Camera-Tilt.vcc, S3.Vcc
  N9: Camera-Tilt.pulse, S3.pulse
  GND_5: Camera-Pan.gnd, S4.gnd
  VCC_5: Camera-Pan.vcc, S4.Vcc
  N10: Camera-Pan.pulse, S4.pulse
  N11: R2.Pin_0, バッテリ電圧.pin2
