# Fritzing sketch id1039_temp_negative_con_amplificazione_0 (saved by Fritzing 0.9.1b)
circuit board: 8.46667cm x 5.64444cm
breadboards: 1

parts:
  Diode_2 = Schottky Diode [part_number=1N5817 package="300 mil [THT]"]
  R1 = Resistor [tolerance=±5% resistance=18k package=THT]
  IC1 = prefix0000 [part_number=TL061]
  R3 = Resistor [tolerance=±5% resistance=56k package=THT]
  Diode_1 = Schottky Diode [part_number=1N5817 package="300 mil [THT]"]
  R5 = Resistor [tolerance=±5% resistance=18k package=THT]
  T1 = TMP36 [package=to-92]
  R6 = Resistor [tolerance=±5% resistance=18k package=THT]
  R7 = Resistor [tolerance=±5% resistance=56k package=THT]
  IC2 = prefix0000 [part_number=TL061]
  Arduino_1 = Arduino Uno (Rev3)

nets:
  N1: Diode_2.cathode, Diode_1.anode
  N2: Diode_2.anode, R1.Pin_1, T1.GND, IC2.connector3
  N3: R1.Pin_0, Diode_1.cathode, R5.Pin_0, R6.Pin_0, Arduino_1.GND
  N4: IC1.connector2, R3.Pin_0, R6.Pin_1
  N5: IC1.connector3, T1.VOUT
  N6: IC1.connector6, R3.Pin_1, Arduino_1.A1
  N7: R5.Pin_1, R7.Pin_0, IC2.connector2
  VCC: T1.VCC, Arduino_1.VIN
  N8: R7.Pin_1, IC2.connector6, Arduino_1.A0

notes:
  Vin: alimentazione TMP (output)
  A1: input amplificato
