# Fritzing sketch id103_2x (saved by Fritzing 0.5.2b)
breadboards: 1

parts:
  U1 = 555 Timer [package="DIP8 [THT]"]
  R3 = Resistor [resistance=1k package=THT]
  C1 = Electrolytic Capacitor [package=THT]
  C2 = Ceramic Capacitor [capacitance=100nF rated_voltage=35V package="100 mil [THT, multilayer]"]
  Parte1 = Copper surface
  S1 = Toggle Switch [package=THT]
  IC1 = IC, DIP package, 16 pins [chip_label=4040 spacing=300mil]
  TRS1 = Stereo Jack (TRS) 3.5mm [package="PG203J [THT]"]
  TRS2 = Stereo Jack (TRS) 3.5mm [package="PG203J [THT]"]
  TRS3 = Stereo Jack (TRS) 3.5mm [package="PG203J [THT]"]
  TRS4 = Stereo Jack (TRS) 3.5mm [package="PG203J [THT]"]
  Power_plug1 = Power plug
  Parte2 = LCD DISPLAY (from obsolete laptops)

nets:
  GND: U1.Ground, C1.-, C2.1, IC1.pin8, IC1.pin11, TRS1.Sleeve, TRS2.Sleeve, TRS3.Sleeve, TRS4.Sleeve, Power_plug1.GND, Parte2.connector0
  N1: U1.Trigger, U1.Threshold, Parte1.connector0, S1.COM
  N2: U1.Output, IC1.pin10, TRS1.Ring, Parte2.connector5
  5V: U1.Reset, U1.Vcc_Supply_Voltage, R3.Pin_0, IC1.pin16, Power_plug1.VCC
  N3: U1.Discharge, R3.Pin_1, Parte1.connector1
  N4: C1.+, S1.L1
  N5: C2.0, S1.L2
  N6: IC1.pin2, TRS4.Tip, Parte2.connector7
  N7: IC1.pin3, TRS3.Ring, Parte2.connector19
  N8: IC1.pin4, Parte2.connector12
  N9: IC1.pin5, TRS3.Tip, Parte2.connector8
  N10: IC1.pin6, TRS2.Ring, Parte2.connector13
  N11: IC1.pin7, TRS2.Tip, Parte2.connector10
  N12: IC1.pin9, TRS1.Tip, Parte2.connector1
  N13: IC1.pin13, TRS4.Ring, Parte2.connector3

notes:
  Éste es el circuito de 2X (ver http://vimeo.com/7033393)
  El timer envía una señal cuya frecuencia es modificada por el contacto de las manos sobre la superficie de cobre. El 4040 divide esta frecuencia generando un patron rítmico. Esta obra usa altavoces de PC. El cable púrpura que sale del 4040 se envía a un subwoofer para un beat bien grave y bajo. Al mismo tiempo que envían señales a los altavoces, esas frecuencias divididas se envían a un display LCD donde generan patrones visuales geométricos audiorítmicos (pintar los contactos en el display con pintura de plata y/o grafito)
  IMPORTANTE: Usar una fuente de alimentación de no más de 5V y 350 mA (debido al uso del cuerpo humano como resistencia variable)
  ADVERTENCIA: PERSONAS CON MARCAPASOS O DEFIBRILADORES NO DEBEN INTERACTUAR CON OBJETOS CUYOS CIRCUITOS UTILICEN AL CUERPO HUMANO COMO RESISTENCIA.
  This is 2X circuit (http://vimeo.com/7033393) . 555 timer sends a signal (square wave) which frequency is modified by hands contact over copper surface. 4040 divides this frequency, obtaining a rhythmic pattern
