# Fritzing sketch id103_3way_rocker_switch_led_control_0 (saved by Fritzing 0.8.7b)
breadboards: 1

parts:
  부품1 = Arduino Uno (Rev3)
  S1 = Toggle Switch [package=THT]
  R1 = Resistor [tolerance=±5% resistance=1k package=THT]
  R2 = Resistor [tolerance=±5% resistance=1k package=THT]
  LED1 = LED - 5mm [color="Yellow (574nm)" package="5 mm [THT]"]
  LED2 = LED - 5mm [color="Green (555nm)" package="5 mm [THT]"]
  R3 = Resistor [tolerance=±5% resistance=220 package=THT]
  R4 = Resistor [tolerance=±5% resistance=220 package=THT]

nets:
  N1: 부품1.D8, R3.Pin_0
  N2: 부품1.D9_PWM, R4.Pin_0
  N3: 부품1.D6_PWM, S1.L2, R2.Pin_1
  N4: 부품1.D7, S1.L1, R1.Pin_1
  N5: 부품1.5V, S1.COM
  N6: 부품1.GND, R1.Pin_0, R2.Pin_0, LED1.cathode, LED2.cathode
  N7: LED1.anode, R3.Pin_1
  N8: LED2.anode, R4.Pin_1
