# Fritzing sketch id1040_CEM_BUILD_0 (saved by Fritzing 0.9.3b)
stripboards: 1

parts:
  IC2 = Dual Op-Amp [package=dip08]
  IC5 = CEM3340
  R1 = Trimmer Potentiometer [maximum_resistance=10kΩ package=THT]
  R2 = Resistor [tolerance=±5% resistance=22k package=THT]
  R3 = Resistor [tolerance=±5% resistance=4.7k package=THT]
  R4 = Resistor [tolerance=±5% resistance=680 package=THT]
  R5 = Resistor [tolerance=±5% resistance=100k package=THT]
  R6 = Resistor [tolerance=±5% resistance=100k package=THT]
  R7 = Resistor [tolerance=±5% resistance=470 package=THT]
  C1 = Ceramic Capacitor [capacitance=10nF package="100 mil [THT, multilayer]"]
  C2 = Ceramic Capacitor [capacitance=1nF package="100 mil [THT, multilayer]"]
  R8 = Resistor [tolerance=±5% resistance=470 package=THT]
  R9 = Resistor [tolerance=±5% resistance=220 package=THT]
  J1 = Power Jack [package=power_jack_pth_lock]
  R11 = Resistor [tolerance=±5% resistance=10k package=THT]
  R10 = Resistor [tolerance=±1% resistance=1M package=THT]
  R12 = Rotary Potentiometer (Small) [maximum_resistance=100kΩ package=THT]
  IC6 = Dual Op-Amp [package=dip08]
  TRS1 = Stereo Jack (TRS) 3.5mm [package="PG203J [THT]"]
  TRS2 = Audio Jack (TRS) 3.5mm [package="4Ucon 08780 [THT]"]
  TRS3 = Audio Jack (TRS) 3.5mm [package="4Ucon 08780 [THT]"]
  TRS5 = Audio Jack (TRS) 3.5mm [package="4Ucon 08780 [THT]"]
  TRS7 = Audio Jack (TRS) 3.5mm [package="4Ucon 08780 [THT]"]  # not connected
  TRS8 = Audio Jack (TRS) 3.5mm [package="4Ucon 08780 [THT]"]
  C3 = Ceramic Capacitor [capacitance=1nF package="100 mil [THT, multilayer]"]
  C4 = Ceramic Capacitor [capacitance=1nF package="100 mil [THT, multilayer]"]
  TRS6 = Audio Jack (TRS) 3.5mm [package="4Ucon 08780 [THT]"]

nets (from the breadboard view):
  N1: IC2.A_OUT, IC2.A_-IN, IC2.A_+IN, IC2.B_-IN, IC2.B_OUT, IC2.A_V+, IC5.connector0, IC5.connector7, IC5.connector8, IC5.connector15, R2.Pin_0, J1.GNDBREAK, R10.Pin_0, R12.leg2, IC6.A_OUT, IC6.A_-IN, IC6.B_OUT, IC6.A_V+, TRS2.Ring, TRS3.Ring, TRS5.Tip, C4.1
  N2: IC2.A_V-, IC2.B_+IN, IC5.connector6, IC5.connector9, R4.Pin_1, J1.GND, IC6.A_V-, IC6.B_+IN
  N3: IC5.connector1, IC5.connector14, R3.Pin_1, R5.Pin_0, R6.Pin_0, R7.Pin_0
  N4: IC5.connector2, IC5.connector13, R1.wiper, R1.leg2, R3.Pin_0, R4.Pin_0, R5.Pin_1, R9.Pin_1, R10.Pin_1
  N5: IC5.connector3, IC5.connector12, R8.Pin_0, R11.Pin_1, IC6.A_+IN, IC6.B_-IN
  N6: IC5.connector4, IC5.connector11, C1.1, C2.1, R8.Pin_1, R9.Pin_0, J1.PWR, R11.Pin_0, TRS1.Ring, TRS6.Ring
  N7: IC5.connector5, IC5.connector10, C2.0, C3.1
  N8: R1.leg1, R2.Pin_1, R12.wiper
  N9: R6.Pin_1, TRS1.Tip
  N10: R7.Pin_1, C1.0
  N11: TRS8.Ring, C3.0

notes:
  Black: -12v
  Orange: Ground
  Red: +12v
  PWM IN
  SAW OUT
  HARD SYNC
  PULSE OUT
  TRIANGLE OUT
  SOFT SYNC
  CV IN
