# Fritzing sketch id1041_CH924_0 (saved by Fritzing 0.9.2b)
breadboards: 1

parts:
  Raspberry_Pi1 = Raspberry Pi 2
  R1 = Resistor [tolerance=±5% resistance=10 package="0603 [SMD]"]

nets:
  N1: Raspberry_Pi1.GPIO21, R1.Pin_0

notes:
  CH924 Coin Machine
  White Wire
  Power Tail
  Ground
