# Fritzing sketch id1042_codigo_arduino (saved by Fritzing 0.9.3b)
breadboards: 1

parts:
  Componente1 = Arduino Uno (Rev3)
  LED1 = LED - 5mm [color="Red (633nm)" package="5 mm [THT]"]
  LED2 = LED - 5mm [color="Red (633nm)" package="5 mm [THT]"]
  LED3 = LED - 5mm [color="Red (633nm)" package="5 mm [THT]"]
  LED4 = LED - 5mm [color="Red (633nm)" package="5 mm [THT]"]
  LED5 = LED - 5mm [color="Red (633nm)" package="5 mm [THT]"]
  LED6 = LED - 5mm [color="Red (633nm)" package="5 mm [THT]"]
  R1 = Resistor [tolerance=±5% resistance=220 package=THT]
  R2 = Resistor [tolerance=±5% resistance=220 package=THT]
  R3 = Resistor [tolerance=±5% resistance=220 package=THT]
  R4 = Resistor [tolerance=±5% resistance=220 package=THT]
  R5 = Resistor [tolerance=±5% resistance=220 package=THT]
  R6 = Resistor [tolerance=±5% resistance=220 package=THT]
  S1 = Pushbutton [package=THT]

nets:
  N1: Componente1.D8, LED2.anode
  N2: Componente1.D9_PWM, LED1.anode
  N3: Componente1.GND, R1.Pin_0, R2.Pin_0, R3.Pin_0, R4.Pin_0, R5.Pin_0, R6.Pin_0, S1.leg1
  N4: Componente1.D3_PWM, S1.leg0
  N5: Componente1.D4, LED6.anode
  N6: Componente1.D5_PWM, LED5.anode
  N7: Componente1.D6_PWM, LED4.anode
  N8: Componente1.D7, LED3.anode
  N9: LED1.cathode, R1.Pin_1
  N10: LED2.cathode, R2.Pin_1
  N11: LED3.cathode, R3.Pin_1
  N12: LED4.cathode, R4.Pin_1
  N13: LED5.cathode, R5.Pin_1
  N14: LED6.cathode, R6.Pin_1
