# Fritzing sketch id1043_Model_0 (saved by Fritzing 0.9.3b)
breadboards: 1

parts:
  Part1 = Arduino Uno (Rev3)
  R1 = Resistor [tolerance=±5% resistance=220 package=THT]
  LED1 = LED - 5mm [color="Red (633nm)" package="5 mm [THT]"]
  R2 = Resistor [tolerance=±5% resistance=220 package=THT]
  S2 = Pushbutton [package=THT]
  S3 = Pushbutton [package=THT]

nets:
  N1: Part1.D8, R2.Pin_1, S2.leg1
  N2: Part1.D9_PWM, R1.Pin_1, S3.leg1
  N3: Part1.D3_PWM, LED1.anode
  N4: Part1.5V, S2.leg0, S3.leg0
  N5: Part1.GND, R1.Pin_0, LED1.cathode, R2.Pin_0

notes:
  The next circuit change the intensity of volts, provided to the LED , with two buttons, Button left DOWN and Button rigth UP.
  COMPONENTS :
  * 3 RESISTENCES
  * 2 PUSH BUTTONS
  * 1 LED
