# Fritzing sketch id1044_RadioShackBoard_Connecting_Poorman_Scope_0 (saved by Fritzing 0.9.0b)
breadboards: 1

parts:
  U9 = prefix_TL082 [part_number=ADTL082]
  R3 = Resistor 2p2k small
  R5 = Resistor 22k small
  R4 = Resistor 22k small
  R6 = Resistor 3p3k small
  R12 = Resistor 3p3k small
  R11 = Resistor 2p2k small
  R9 = Resistor 1k small
  R8 = Resistor 1k small
  R7 = Resistor_100_small
  R2 = Resistor_220_Small
  R1 = Resistor_220_Small
  R14 = Resistor_220_Small
  R13 = Resistor_220_Small
  SW1 = PREFIX_DPDT
  BAT1 = Battery block 9V
  BAT2 = Battery block 9V
  LED2 = LED - 5mm [color="Yellow (585nm)" package="5 mm [THT]"]
  LED1 = LED - 5mm [color="Yellow (585nm)" package="5 mm [THT]"]
  R10 = POT [package=pot_alpha_rv16af-20]
  R = POT [package=pot_alpha_rv16af-20]
  C = Ceramic Capacitor [capacitance=2.2µF package="100 mil [THT, multilayer]"]
  C2 = Ceramic Capacitor [capacitance=100nF package="100 mil [THT, multilayer]"]
  C1 = Ceramic Capacitor [capacitance=10nF package="100 mil [THT, multilayer]"]
  U9_2 = prefix_TL082 [part_number=ADTL082]
  U9_1 = prefix_TL082 [part_number=ADTL082]
  U10 = prefix_TL082 [part_number=ADTL082]
  U10_1 = prefix_TL082 [part_number=ADTL082]
  U10_2 = prefix_TL082 [part_number=ADTL082]
  R15 = Resistor [tolerance=±5% resistance=1M package=THT]
  R16 = Resistor [tolerance=±5% resistance=1M package=THT]
  JP1 = RCA [package=rca]
  JP2 = RCA [package=rca]

nets:
  N1: U9.connector1, R8.connector1, R7.connector1, U9_1.connector1
  N2: U9.connector2, U9.connector6, R9.connector1, R8.connector0, U9_2.connector6, U9_1.connector2
  N3: U9.connector3, R11.connector0, R10.S, C.0, U9_1.connector3
  -9V: U9.connector4, R14.connector0, SW1.connector1, U9_1.connector4, U10.connector4, U10_1.connector4
  N4: U9.connector5, R12.connector0, R7.connector0, R.S, C2.1, U9_2.connector5, R15.Pin_1
  N5: U9.connector7, R9.connector0, C.1, U9_2.connector7
  +9V: U9.connector8, R13.connector0, SW1.connector5, U9_1.connector8, U10.connector8, U10_1.connector8
  GND: R3.connector0, R6.connector1, R11.connector1, BAT1.-, BAT2.+, LED2.anode, LED1.anode, R10.A, C2.0, C1.0, JP1.SHELL, JP2.SHELL
  N6: R3.connector1, R2.connector0, U10.connector6, U10_2.connector6
  N7: R5.connector0, R4.connector0, U10.connector1, U10_1.connector1
  N8: R5.connector1, R6.connector0, U10.connector2, U10_1.connector2
  N9: R4.connector1, R12.connector1, R1.connector0, R.A, C1.1, U10.connector3, U10.connector5, U10_1.connector3, U10_2.connector5, R16.Pin_1
  N10: R2.connector1, R1.connector1, U10.connector7, U10_2.connector7
  N11: R14.connector1, LED2.cathode
  N12: R13.connector1, LED1.cathode
  N13: SW1.connector0, BAT2.-
  N14: SW1.connector6, BAT1.+
  N15: R15.Pin_0, JP1.PIN
  N16: R16.Pin_0, JP2.PIN

notes:
  .
  Chua's Circuit to Poorman's Scope
