# Fritzing sketch id1045_Untitled_Sketch_0 (saved by Fritzing 0.9.1b)
circuit board: 4.78367cm x 2.52588cm
breadboards: 1

parts:
  D1 = Diode [part_number=1N4007 package=diode-1n4148]
  R1 = Resistor [tolerance=±5% resistance=180 package=THT]
  R2 = Resistor [tolerance=±5% resistance=1k package=THT]
  ZD = Zener Diode [part_number="6,8V / 1W" breakdown_voltage=6.8 package="300 mil [THT]"]
  V1 = DC Power [voltage=12V]
  R3 = Resistor [tolerance=±5% resistance=10 package="1206 [SMD]"]
  D2 = Diode [part_number=1N4007 package=diode-1n4001]
  Q1 = NPN-Transistor [part_number=BC548 package="TO92 [THT]"]
  R4 = Trimmer Potentiometer [maximum_resistance=1kΩ package=THT]
  U1 = V_REG_MC33269 [package=dpak]
  solar_- = Pad [width=2.82222222222222 height=2.82222222222222 connect=center]
  solar_+ = Pad [width=2.82222222222222 height=3.24555555555556 connect=center]
  + = Pad [width=2.25777777777778 height=2.11666666666667 connect=center]
  - = Pad [width=2.54 height=2.25777777777778 connect=center]

nets:
  N1: D1.A, V1.V+, solar_+.pad
  N2: D1.C, U1.IN
  N3: R1.Pin_0, D2.A, U1.OUT
  N4: R1.Pin_1, Q1.C, R4.leg1, R4.wiper, U1.GND
  N5: R2.Pin_0, Q1.B
  N6: R2.Pin_1, ZD.anode
  N7: ZD.cathode, R3.Pin_1, +.pad
  N8: V1.V-, Q1.E, R4.leg2, solar_-.pad, -.pad
  N9: R3.Pin_0, D2.C
