# Fritzing sketch id1046_Untitled_Sketch_1_0 (saved by Fritzing 0.9.1b)
circuit board: 5.30827cm x 2.43024cm
breadboards: 1

parts:
  S1 = SPST Switch [package=switch-spdt-smd]
  IC1 = Voltage Regulator [package=to220-igo]
  C1 = Ceramic Capacitor [capacitance="100 nF" package="0805 [SMD, multilayer]"]
  C2 = Capacitor Polarized [package=panasonic_g]
  Pad1 = Pad [width=3.22770155068937 height=3.01734207948094 connect=center]
  X1 = USB Connectors [package=usb-a-s-silk-female]
  Pad2 = Pad [width=5.01336603081914 height=3.12894610948904 connect=center]

nets:
  N1: S1.O, IC1.IN, C2.+
  N2: S1.P, Pad1.pad
  N3: IC1.OUT, C1.1, X1.D+
  N4: C1.0, C2.-, X1.GND, Pad2.pad
