# Fritzing sketch id1046_knight_rider_with_16f627A (saved by Fritzing 0.6.3b)
breadboards: 1

parts:
  R1 = Resistor [tolerance=±5% resistance=220 package=THT]
  R2 = Resistor [tolerance=±5% resistance=220 package=THT]
  R3 = Resistor [tolerance=±5% resistance=220 package=THT]
  R4 = Resistor [tolerance=±5% resistance=220 package=THT]
  LED1 = LED - 5mm [color="Red (633nm)" package="5 mm [THT]"]
  LED2 = LED - 5mm [color="Red (633nm)" package="5 mm [THT]"]
  LED3 = LED - 5mm [color="Red (633nm)" package="5 mm [THT]"]
  LED4 = LED - 5mm [color="Red (633nm)" package="5 mm [THT]"]
  VCC1 = 4 x AAA Battery Mount [part_number="4.8 V"]
  J1 = female pin header, 5 pins [form="♂ (male)" part_number="PICkit2 connection"]
  LED5 = LED - 5mm [color="Red (633nm)" package="5 mm [THT]"]
  R5 = Resistor [tolerance=±5% resistance=220 package=THT]
  IC1 = IC, DIP package, 18 pins [chip_label="PIC 16F627A" spacing=300mil]

nets:
  N1: R1.Pin_0, LED4.cathode
  N2: R1.Pin_1, IC1.pin3
  N3: R2.Pin_0, LED3.cathode
  N4: R2.Pin_1, IC1.pin2
  N5: R3.Pin_0, LED2.cathode
  N6: R3.Pin_1, IC1.pin1
  N7: R4.Pin_0, LED1.cathode
  N8: R4.Pin_1, IC1.pin18
  N9: LED1.anode, LED2.anode, LED3.anode, LED4.anode, VCC1.-, J1.pin3, LED5.anode, IC1.pin5
  N10: VCC1.+, J1.pin4, IC1.pin14
  N11: J1.pin1, IC1.pin12
  N12: J1.pin2, IC1.pin13
  N13: LED5.cathode, R5.Pin_0
  N14: R5.Pin_1, IC1.pin17
