# Fritzing sketch id1047_Charlie20SnowzijkantSO08_EIAJ_29cm_0 (saved by Fritzing 0.7.11b)
breadboards: 1

parts:
  LED8 = LED - 3mm [color="White (6500K)" package="3 mm [THT]"]
  LED7 = LED - 3mm [color="White (6500K)" package="3 mm [THT]"]
  LED6 = LED - 3mm [color="White (6500K)" package="3 mm [THT]"]
  LED20 = LED - 3mm [color="White (6500K)" package="3 mm [THT]"]
  LED19 = LED - 3mm [color="White (6500K)" package="3 mm [THT]"]
  LED18 = LED - 3mm [color="White (6500K)" package="3 mm [THT]"]
  LED17 = LED - 3mm [color="White (6500K)" package="3 mm [THT]"]
  LED16 = LED - 3mm [color="White (6500K)" package="3 mm [THT]"]
  LED15 = LED - 3mm [color="White (6500K)" package="3 mm [THT]"]
  LED14 = LED - 3mm [color="White (6500K)" package="3 mm [THT]"]
  LED13 = LED - 3mm [color="White (6500K)" package="3 mm [THT]"]
  LED12 = LED - 3mm [color="White (6500K)" package="3 mm [THT]"]
  LED9 = LED - 3mm [color="White (6500K)" package="3 mm [THT]"]
  LED10 = LED - 3mm [color="White (6500K)" package="3 mm [THT]"]
  LED11 = LED - 3mm [color="White (6500K)" package="3 mm [THT]"]
  LED5 = LED - 3mm [color="White (6500K)" package="3 mm [THT]"]
  LED4 = LED - 3mm [color="White (6500K)" package="3 mm [THT]"]
  LED3 = LED - 3mm [color="White (6500K)" package="3 mm [THT]"]
  LED2 = LED - 3mm [color="White (6500K)" package="3 mm [THT]"]
  LED1 = LED - 3mm [color="White (6500K)" package="3 mm [THT]"]
  C1 = Ceramic Capacitor [capacitance=100nF part_number="Farnell: 1740665RL" package="0805 [SMD, multilayer]"]
  R1 = Resistor [tolerance=±5% resistance=100 package="0805 [SMD]"]
  R2 = Resistor [tolerance=±5% resistance=100 package="0805 [SMD]"]
  R3 = Resistor [tolerance=±5% resistance=100 package="0805 [SMD]"]
  R4 = Resistor [tolerance=±5% resistance=100 package="0805 [SMD]"]
  R5 = Resistor [tolerance=±5% resistance=100 package="0805 [SMD]"]
  MOSI = Pad [width=2 height=3 connect=north]
  Vcc = Pad [width=2 height=3 connect=north]
  SCK = Pad [width=2 height=3 connect=north]
  *GND = Pad [width=2 height=3 connect=north]
  *RST = Pad [width=2 height=3 connect=north]
  *MISO = Pad [width=2 height=3 connect=north]
  ATTiny45 = SO08-EIAJ [chip_label=SO08 part_number="Farnell: 1288353" package=SO]
  5V_DC = longpad pin header, 2 pins [form="long pad"]

nets:
  yellow: LED8.cathode, LED16.cathode, LED12.cathode, LED4.cathode, R5.Pin_0, SCK.pad, ATTiny45.7
  N1: LED8.anode, LED7.anode, LED6.anode, LED5.anode, R2.Pin_1
  blue: LED7.cathode, LED20.cathode, LED11.cathode, LED3.cathode, R4.Pin_0, *MISO.pad, ATTiny45.6
  white: LED6.cathode, LED19.cathode, LED15.cathode, LED2.cathode, R3.Pin_0, MOSI.pad, ATTiny45.5
  N2: LED20.anode, LED19.anode, LED18.anode, LED17.anode, R5.Pin_1
  orange: LED18.cathode, LED14.cathode, LED10.cathode, LED1.cathode, R2.Pin_0, ATTiny45.3
  green: LED17.cathode, LED13.cathode, LED9.cathode, LED5.cathode, R1.Pin_0, ATTiny45.2
  N3: LED16.anode, LED15.anode, LED14.anode, LED13.anode, R4.Pin_1
  N4: LED12.anode, LED9.anode, LED10.anode, LED11.anode, R3.Pin_1
  N5: LED4.anode, LED3.anode, LED2.anode, LED1.anode, R1.Pin_1
  GND: C1.0, *GND.pad, ATTiny45.4, 5V_DC.pin1
  5V: C1.1, Vcc.pad, ATTiny45.8, 5V_DC.pin2
  N6: *RST.pad, ATTiny45.1

notes:
  -
  (*=bottom side)
  + -
  By Davy Uittenbogerd - Ver 1.0
  Please, go to the scheme and PCB view.
  This breadbord view would be to messy with this much connections.
