# Fritzing sketch id1048_Motor_com_fim_de_curso_0 (saved by Fritzing 0.9.3b)
breadboards: 1

parts:
  S1 = SWITCH-DPDT [package=eg2211]
  V1 = DC Power [voltage=5]
  M1 = DC Motor
  S2 = Toggle Switch [package=THT]
  S3 = Toggle Switch [package=THT]
  LED1 = LED - 5mm [color="Green (570nm)" package="5 mm [THT]"]
  LED2 = LED - 5mm [color="Red (633nm)" package="5 mm [THT]"]
  R1 = Resistor [tolerance=±5% resistance=220 package=THT]
  R2 = Resistor [tolerance=±5% resistance=220 package=THT]

nets:
  N1: S1.2, V1.V+
  N2: S1.1, S2.COM
  N3: S1.3, M1.pin_1, S3.L2, LED2.cathode, R1.Pin_1
  N4: S1.6, M1.pin_2, S2.L1, LED1.cathode, R2.Pin_0
  N5: S1.4, S3.COM
  N6: S1.5, V1.V-
  N7: LED1.anode, R1.Pin_0
  N8: LED2.anode, R2.Pin_1

notes:
  Canal
  Eletrônica e tecnologia
