# Fritzing sketch id1049_double_168_0 (saved by Fritzing 0.4.2b)
breadboards: 5

parts:
  IC1 = IC, SIP package, 30 pins [chip_label="Clock Face" spacing=300mil]
  U4 = atmega168 [package="DIP28 [THT]"]
  R1 = Resistor [resistance=10k package=THT]
  S3 = Pushbutton [package="[THT]"]
  J1 = female pin header, 14 pins [form="♀ (female)"]
  J1_2 = female pin header, 14 pins [form="♀ (female)"]
  J2 = female pin header, 5 pins [form="♀ (female)"]
  R1_2 = Resistor [resistance=10k package=THT]
  U4_2 = atmega168 [package="DIP28 [THT]"]
  S3_2 = Pushbutton [package="[THT]"]
  J1_3 = female pin header, 14 pins [form="♀ (female)"]
  J1_4 = female pin header, 14 pins [form="♀ (female)"]
  J2_2 = female pin header, 5 pins [form="♀ (female)"]
  R2 = Resistor [resistance=220 package=THT]
  R2_2 = Resistor [resistance=220 package=THT]
  R3 = Resistor [resistance=10k package=THT]
  R3_2 = Resistor [resistance=10k package=THT]
  U5 = Voltage Regulator - 5V [package="TO220 [THT]"]
  Power_plug1 = Power plug

nets:
  N1: IC1.pin1, R2_2.Pin_0
  N2: IC1.pin2, R2.Pin_0
  N3: IC1.pin5, U4.Pin_10, J1_2.pin10
  N4: IC1.pin9, U4.Pin_2, J1_2.pin2
  N5: IC1.pin10, U4.Pin_3, J1_2.pin3
  N6: IC1.pin12, U4.Pin_4, J1_2.pin4
  N7: IC1.pin13, U4.Pin_5, J1_2.pin5
  N8: IC1.pin15, U4.Pin_6, J1_2.pin6
  N9: IC1.pin16, U4.Pin_11, J1_2.pin11
  N10: IC1.pin17, U4.Pin_12, J1_2.pin12
  N11: IC1.pin18, U4.Pin_13, J1_2.pin13
  N12: IC1.pin19, U4.Pin_14, J1_2.pin14
  N13: IC1.pin20, U4.Pin_15, J1.pin14
  N14: IC1.pin21, U4.Pin_16, J1.pin13
  N15: IC1.pin30, U4.Pin_9, J1_2.pin9
  N16: U4.Pin_1, R1.Pin_0, S3.Pin_1, S3.Pin_2, J1_2.pin1, J2.pin5
  N17: U4.Pin_7, U4.Pin_20, R1.Pin_1, J1.pin9, J1_2.pin7, R1_2.Pin_1, U4_2.Pin_7, U4_2.Pin_20, J1_3.pin7, J1_4.pin9, R3.Pin_1, R3_2.Pin_1, U5.output_voltage
  GND: U4.Pin_8, U4.Pin_22, S3.Pin_3, S3.Pin_4, J1.pin7, J1_2.pin8, J2.pin1, U4_2.Pin_8, U4_2.Pin_22, S3_2.Pin_3, S3_2.Pin_4, J1_3.pin8, J1_4.pin7, J2_2.pin1, U5.GND, Power_plug1.GND
  N18: U4.Pin_17, J1.pin12, J2.pin4
  N19: U4.Pin_18, J1.pin11, J2.pin3
  N20: U4.Pin_19, J1.pin10, J2.pin2
  N21: U4.Pin_21, J1.pin8
  N22: U4.Pin_23, J1.pin6, R2.Pin_1
  N23: U4.Pin_24, J1.pin5, R2_2.Pin_1
  N24: U4.Pin_25, J1.pin4
  N25: U4.Pin_26, J1.pin3
  N26: U4.Pin_27, J1.pin2, U4_2.Pin_27, J1_4.pin2, R3_2.Pin_0
  N27: U4.Pin_28, J1.pin1, U4_2.Pin_28, J1_4.pin1, R3.Pin_0
  N28: R1_2.Pin_0, U4_2.Pin_1, S3_2.Pin_1, S3_2.Pin_2, J1_3.pin1, J2_2.pin5
  N29: U4_2.Pin_2, J1_3.pin2
  N30: U4_2.Pin_3, J1_3.pin3
  N31: U4_2.Pin_4, J1_3.pin4
  N32: U4_2.Pin_5, J1_3.pin5
  N33: U4_2.Pin_6, J1_3.pin6
  N34: U4_2.Pin_9, J1_3.pin9
  N35: U4_2.Pin_10, J1_3.pin10
  N36: U4_2.Pin_11, J1_3.pin11
  N37: U4_2.Pin_12, J1_3.pin12
  N38: U4_2.Pin_13, J1_3.pin13
  N39: U4_2.Pin_14, J1_3.pin14
  N40: U4_2.Pin_15, J1_4.pin14
  N41: U4_2.Pin_16, J1_4.pin13
  N42: U4_2.Pin_17, J1_4.pin12, J2_2.pin4
  N43: U4_2.Pin_18, J1_4.pin11, J2_2.pin3
  N44: U4_2.Pin_19, J1_4.pin10, J2_2.pin2
  N45: U4_2.Pin_21, J1_4.pin8
  N46: U4_2.Pin_23, J1_4.pin6
  N47: U4_2.Pin_24, J1_4.pin5
  N48: U4_2.Pin_25, J1_4.pin4
  N49: U4_2.Pin_26, J1_4.pin3
  N50: U5.input_voltage, Power_plug1.VCC

notes:
  Reset Switch
  Programming Port
  Atmega 168 Powering The Clock Face
  Atmega 168 Controlling the Other via I2C
  Clock Face dug out of an ancient digital alarm clock
  I2C Bus
  Power
