# Fritzing sketch id104_3144_0 (saved by Fritzing 0.9.2b)
breadboards: 1

parts:
  Bauteil1 = Arduino Uno (Rev3)
  R1 = Resistor [tolerance=±5% resistance=10k package=THT]
  Q1 = PNP-Transistor [part_number=3144 package="SOT-23 [SMD]"]

nets:
  N1: Bauteil1.GND, Q1.0
  N2: Bauteil1.D2, R1.Pin_1, Q1.1
  N3: Bauteil1.5V, R1.Pin_0, Q1.2
