# Fritzing sketch id1050_Check_Temperature_0 (saved by Fritzing 0.9.3b)
breadboards: 1

parts:
  Composant1 = Arduino Uno (Rev3)
  R1 = Resistor [tolerance=±5% resistance=220 package=THT]
  R2 = Resistor [tolerance=±5% resistance=220 package=THT]
  R3 = Resistor [tolerance=±5% resistance=220 package=THT]
  LED1 = LED - 5mm [color="Red (633nm)" package="5 mm [THT]"]
  LED2 = LED - 5mm [color="Red (633nm)" package="5 mm [THT]"]
  LED3 = LED - 5mm [color="Red (633nm)" package="5 mm [THT]"]
  T1 = LM35 Temperature Sensor [package="TO92 [THT]"]

nets:
  N1: Composant1.A0, T1.Vout
  GND: Composant1.GND, R1.Pin_0, R2.Pin_0, R3.Pin_0, T1.GND
  N2: Composant1.D2, LED1.anode
  N3: Composant1.D3_PWM, LED2.anode
  N4: Composant1.D4, LED3.anode
  N5: Composant1.5V, T1.+Vs
  N6: R1.Pin_1, LED3.cathode
  N7: R2.Pin_1, LED2.cathode
  N8: R3.Pin_1, LED1.cathode
