# Fritzing sketch id1051_Cheerlights_0 (saved by Fritzing 0.9.1b)
circuit board: 8.46667cm x 5.64444cm
breadboards: 1

parts:
  Part1 = Spark Core (v1.0)
  R1 = Resistor [tolerance=±5% resistance=220 package=THT]
  NEOPIXEL1 = Neopixel_8x8_Matrix
  BB1 = 8_Line_Bi_Directional_Level_Shifter
  J2 = Power Jack [package=power_jack_pth]
  C1 = Capacitor Polarized [package=cpol-radial-1000uf-25v]

nets:
  GND: Part1.GND, NEOPIXEL1.connector3, BB1.connector20, J2.GND, C1.-
  5V: Part1.VIN, NEOPIXEL1.connector2, BB1.connector11, J2.PWR, C1.+
  N1: Part1.D6, BB1.connector2
  N2: Part1.3V3, BB1.connector1, BB1.connector10
  N3: R1.Pin_0, BB1.connector12
  N4: R1.Pin_1, NEOPIXEL1.connector1

notes:
  Connect jack to 2A 5VDC power supply
  TXB0104
  level
  shifter
