# Fritzing sketch id1052_Cheese_0 (saved by Fritzing 0.9.1b)
breadboards: 1

parts:
  Part1 = Arduino Uno (Rev3)
  BAT1 = BC9VPC [package=bc9vpc]
  R1 = PHOTOCELL [package=photocell]
  R2 = Resistor [tolerance=±5% resistance=10k package=THT]
  LED1 = LEDs [package=led10mm]

nets:
  N1: Part1.A0, Part1.D11_PWM/MOSI, R1.P$1, R2.Pin_1, LED1.C
  N2: Part1.GND, R2.Pin_0, LED1.A
  N3: Part1.5V, R1.P$2
  N4: BAT1.V+, BAT1.V-
