# Fritzing sketch id1053_Chenillard_shield3_0 (saved by Fritzing 0.9.2b)
circuit board: 5.18569cm x 4.91769cm
breadboards: 1

parts:
  S2 = Toggle Switch [package=THT]
  LED1 = LED - 5mm [color="Red (633nm)" package="5 mm [THT]"]
  LED2 = LED - 5mm [color="Red (633nm)" package="5 mm [THT]"]
  LED3 = LED - 5mm [color="Red (633nm)" package="5 mm [THT]"]
  LED4 = LED - 5mm [color="Red (633nm)" package="5 mm [THT]"]
  LED5 = LED - 5mm [color="Red (633nm)" package="5 mm [THT]"]
  LED6 = LED - 5mm [color="Red (633nm)" package="5 mm [THT]"]
  LED7 = LED - 5mm [color="Red (633nm)" package="5 mm [THT]"]
  R1 = Resistor [tolerance=±5% resistance=220 package=THT]
  R2 = Resistor [tolerance=±5% resistance=220 package=THT]
  R3 = Resistor [tolerance=±5% resistance=220 package=THT]
  R4 = Resistor [tolerance=±5% resistance=220 package=THT]
  R5 = Resistor [tolerance=±5% resistance=220 package=THT]
  R6 = Resistor [tolerance=±5% resistance=220 package=THT]
  R7 = Resistor [tolerance=±5% resistance=220 package=THT]
  R8 = Resistor [tolerance=±5% resistance=220 package=THT]
  LED8 = LED - 5mm [color="Red (633nm)" package="5 mm [THT]"]
  R9 = Resistor [tolerance=±5% resistance=220 package=THT]
  R10 = Resistor [tolerance=±5% resistance=220 package=THT]
  R11 = Trimmer Potentiometer [maximum_resistance=10kΩ package=THT]
  Composant2 = Arduino Uno (Rev3)
  S4 = Pushbutton [package="[THT]"]

nets (from the schematic view):
  N1: S2.L1, LED1.cathode, LED2.cathode, LED3.cathode, LED4.cathode, LED5.cathode, LED6.cathode, LED7.cathode, LED8.cathode, R11.leg1, Composant2.GND, S4.Pin_1, S4.Pin_2
  N2: S2.COM, R10.Pin_0, Composant2.A5/SCL
  N3: LED1.anode, R8.Pin_1
  N4: LED2.anode, R7.Pin_1
  N5: LED3.anode, R6.Pin_1
  N6: LED4.anode, R5.Pin_1
  N7: LED5.anode, R4.Pin_1
  N8: LED6.anode, R3.Pin_1
  N9: LED7.anode, R2.Pin_1
  N10: R1.Pin_0, Composant2.D0/RX
  N11: R1.Pin_1, LED8.anode
  N12: R2.Pin_0, Composant2.D1/TX
  N13: R3.Pin_0, Composant2.D2
  N14: R4.Pin_0, Composant2.D3_PWM
  N15: R5.Pin_0, Composant2.D4
  N16: R6.Pin_0, Composant2.D5_PWM
  N17: R7.Pin_0, Composant2.D6_PWM
  N18: R8.Pin_0, Composant2.D7
  N19: R9.Pin_0, Composant2.A4/SDA, S4.Pin_3
  N20: R9.Pin_1, R10.Pin_1, R11.leg2, Composant2.5V
  N21: R11.wiper, Composant2.A3

notes:
  Thomas AUBERT
