# Fritzing sketch id1054_Chenillard_0 (saved by Fritzing 0.9.1b)
breadboards: 1

parts:
  Composant1 = Arduino Uno (Rev3)
  LED1 = LED - 5mm [color="Red (633nm)" package="5 mm [THT]"]
  LED2 = LED - 5mm [color="Orange (605nm)" package="5 mm [THT]"]
  LED3 = LED - 5mm [color="Blue (470nm)" package="5 mm [THT]"]
  LED4 = LED - 5mm [color="Orange (605nm)" package="5 mm [THT]"]
  LED5 = LED - 5mm [color="Red (633nm)" package="5 mm [THT]"]
  R1 = Resistor [tolerance=±0.25% resistance=1k package=THT]
  R2 = Resistor [tolerance=±0.25% resistance=1k package=THT]
  R3 = Resistor [tolerance=±0.25% resistance=1k package=THT]
  R4 = Resistor [tolerance=±0.25% resistance=1k package=THT]
  R5 = Resistor [tolerance=±0.25% resistance=1k package=THT]

nets:
  N1: Composant1.D8, R1.Pin_1
  N2: Composant1.D9_PWM, R2.Pin_1
  N3: Composant1.D10_PWM/SS, R3.Pin_1
  N4: Composant1.D11_PWM/MOSI, R4.Pin_1
  N5: Composant1.D12/MISO, R5.Pin_1
  N6: Composant1.GND, LED1.cathode, LED2.cathode, LED3.cathode, LED4.cathode, LED5.cathode
  N7: LED1.anode, R1.Pin_0
  N8: LED2.anode, R2.Pin_0
  N9: LED3.anode, R3.Pin_0
  N10: LED4.anode, R4.Pin_0
  N11: LED5.anode, R5.Pin_0
