# Fritzing sketch id1057_Chicken_coop_door_v3_0 (saved by Fritzing 0.9.3b)
breadboards: 1

parts:
  Part1 = Arduino Uno (Rev3)
  U3 = 2ChannelRelay
  S3 = Reed switch [package=THT]
  S4 = Reed switch [package=THT]
  M1 = DC Motor
  LED1 = LED - 5mm [color="Red (633nm)" package="5 mm [THT]"]
  LED2 = LED - 5mm [color="Yellow (595nm)" package="5 mm [THT]"]
  LED3 = LED - 5mm [color="Green (570nm)" package="5 mm [THT]"]
  VCC2 = 4 x AAA Battery Mount
  LED4 = LED - 5mm [color="Red (660nm)" package="5 mm [THT]"]
  R6 = Resistor [tolerance=±5% resistance=1k package=THT]
  R7 = Resistor [tolerance=±5% resistance=1k package=THT]
  R8 = Resistor [tolerance=±5% resistance=1k package=THT]
  R9 = Resistor [tolerance=±5% resistance=1k package=THT]
  R5 = PHOTOCELL [package=photocell]
  S2 = Ponte-H L298N
  S5 = Reed switch [package=THT]
  VCC3 = 4 x AAA Battery Mount

nets:
  N1: Part1.A0, R9.Pin_1, R5.P$1
  N2: Part1.D8, S2.connector5
  N3: Part1.D9_PWM, S2.connector4
  N4: Part1.D11_PWM/MOSI, LED1.anode
  N5: Part1.D12/MISO, LED2.anode
  N6: Part1.D13/SCK, LED3.anode
  N7: Part1.D2, S5.pin_2
  N8: Part1.D3_PWM, S3.pin_2
  N9: Part1.D4, S4.pin_2
  N10: Part1.D6_PWM, U3.connector2
  N11: Part1.D7, S2.connector6
  N12: Part1.5V, U3.connector0, S3.pin_1, S4.pin_1, R5.P$2, S2.connector3, S5.pin_1
  N13: Part1.GND, U3.connector1, R6.Pin_0, R7.Pin_0, R8.Pin_0, R9.Pin_0, S2.connector2, VCC3.-
  N14: U3.connector7, LED4.cathode
  N15: U3.connector8, VCC2.-
  N16: M1.pin_1, S2.connector14
  N17: M1.pin_2, S2.connector13
  N18: LED1.cathode, R8.Pin_1
  N19: LED2.cathode, R7.Pin_1
  N20: LED3.cathode, R6.Pin_1
  N21: VCC2.+, LED4.anode
  N22: S2.connector1, VCC3.+

notes:
  Door Closed Sensor
  (Sodial 013819)
  Door Open Sensor
  (Sodial 013819)
  Obstruction Sensor
  (Sodial 013819)
  12V Power Supply
  (Supply for LED Strip)
  1 Meter 12V Red LED Strip /w Resistors
  CAT5
  24V 4A AC to DC Power Supply
  To power Motor
  (Drok 090233)
  Dual H-Bridge Motor Controller
  (Yeeco 1200085)
  Note: This device also supplies 5V to system
  12/24V Sirplus Motor from Princess Auto
  (SKU: 8291700)
