# Fritzing sketch id1058_Chicken_Door_0 (saved by Fritzing 0.9.3b)
breadboards: 1

parts:
  Part1 = Arduino Mega 2560 (Rev3)
  S1 = Pushbutton [package="[THT]"]
  S2 = Pushbutton [package="[THT]"]
  S3 = Pushbutton [package="[THT]"]
  S4 = Pushbutton [package="[THT]"]
  U3 = LCD-16X2 [package=lcd-16x2_nosilk]
  M1 = DC Motor
  U6 = L298_BRIDGE_DRIVER [package=powerso20]
  LED1 = LED - 3mm [color="Green (560nm)" package="3 mm [THT]"]
  LED2 = LED - 3mm [color="Red (633nm)" package="3 mm [THT]"]
  LED3 = LED - 3mm [color="Blue (430nm)" package="3 mm [THT]"]
  Adafruit_HUZZAH_ESP8266_Breakout1 = Adafruit HUZZAH ESP8266 Breakout [part_number=2471]
  Power_plug1 = Power plug  # not connected
  R1 = PHOTOCELL [package=photocell-kit]
  Power_plug2 = Power plug
  R2 = Rotary Potentiometer (Small) [maximum_resistance=100kΩ package=THT]
  R3 = Resistor [tolerance=±5% resistance=220 package="0402 [SMD]"]
  R4 = Resistor [tolerance=±5% resistance=1M package="0603 [SMD]"]
  R6 = Resistor [tolerance=±5% resistance=1M package="0603 [SMD]"]
  R7 = Resistor [tolerance=±5% resistance=1M package="0603 [SMD]"]
  R8 = Resistor [tolerance=±5% resistance=1M package="0603 [SMD]"]
  R9 = Resistor [tolerance=±5% resistance=10k package=THT]
  R10 = Resistor [tolerance=±5% resistance=220 package=THT]
  R11 = Resistor [tolerance=±5% resistance=220 package=THT]
  R12 = Resistor [tolerance=±5% resistance=220 package=THT]
  S6 = Reed switch [package=THT]
  S7 = Reed switch [package=THT]
  R13 = Resistor [tolerance=±5% resistance=220 package="1206 [SMD]"]
  R14 = Resistor [tolerance=±5% resistance=220 package="1206 [SMD]"]
  S8 = Reed switch [package=THT]
  S9 = Reed switch [package=THT]

nets:
  N1: Part1.A0, R1.P$2, R9.Pin_0
  GND: Part1.GND, U3.VSS, U3.R_W, U3.K, U6.NC, Adafruit_HUZZAH_ESP8266_Breakout1.GND, R2.leg1, R4.Pin_1, R6.Pin_1, R8.Pin_1, R9.Pin_1, R10.Pin_1, R11.Pin_1, R12.Pin_1, S7.pin_2
  N2: Part1.D12_PWM, U3.RS
  N3: Part1.D11_PWM, U3.E
  N4: Part1.D9_PWM, S6.pin_1
  N5: Part1.D8_PWM, S7.pin_1
  N6: Part1.3V3, Adafruit_HUZZAH_ESP8266_Breakout1.V+
  5V: Part1.5V, Part1.D50, Part1.D51, S1.Pin_3, S1.Pin_4, S2.Pin_3, S2.Pin_4, S4.Pin_3, S4.Pin_4, U3.VDD, U6.SENSE_B, R1.P$1, R2.leg2, R3.Pin_1, S8.pin_2, S9.pin_2
  N7: Part1.D0_RX0, Adafruit_HUZZAH_ESP8266_Breakout1.TX
  N8: Part1.D1_TX0, Adafruit_HUZZAH_ESP8266_Breakout1.RX
  N9: Part1.D2_PWM, U3.DB7
  N10: Part1.D3_PWM, U3.DB6
  N11: Part1.D4_PWM, U3.DB5
  N12: Part1.D5_PWM, U3.DB4
  N13: Part1.D7_PWM, U6.GND
  N14: Part1.D22, R14.Pin_0
  N15: Part1.D23, R13.Pin_0
  N16: Part1.D47, LED1.anode
  N17: Part1.D48, LED3.cathode
  N18: Part1.D49, LED2.anode
  N19: Part1.D52, S2.Pin_1, S2.Pin_2, R4.Pin_0
  N20: Part1.D53, S1.Pin_1, S1.Pin_2, R6.Pin_0
  N21: S3.Pin_1, R7.Pin_0
  N22: S4.Pin_1, S4.Pin_2, R8.Pin_0
  N23: U3.VO, R2.wiper
  N24: U3.A, R3.Pin_0
  N25: M1.pin_1, U6.IN2
  N26: M1.pin_2, U6.ENA
  N27: U6.SENSE_A, S6.pin_2
  VSS: U6.VSS, Power_plug2.VCC
  N28: U6.IN3, Power_plug2.GND
  N29: LED1.cathode, R12.Pin_0
  N30: LED2.cathode, R11.Pin_0
  N31: LED3.anode, R10.Pin_0
  N32: R13.Pin_1, S9.pin_1
  N33: R14.Pin_1, S8.pin_1

notes:
  Enable A
  These are the switches for the Green (Open) and Blue (Closed) indicator lights
  These are the switches stopping the door from over opening or over closing
