# Fritzing sketch id1059_Chiliduino_001_0 (saved by Fritzing 0.7.10b)
breadboards: 1

parts:
  Chiliduino-001 = Arduino
  SOIL_MOISTURE_SENSOR = mystery part, 3 pins [chip_label="Soil Moisture Sensor"]
  SOIL_TEMPERATURE_SENSOR = mystery part, 3 pins [chip_label="Soil Temperature Sensor"]
  AIR_TEMPERATURE_HUMIDITY_SENSOR = mystery part, 3 pins [chip_label="Air Temperature and Humidity Sensor"]
  WIFI = LED - 5mm [color="Blue (430nm)" package="5 mm [THT]"]
  220 = Resistor [tolerance=±5% resistance=220 package=THT]
  READ = LED - 5mm [color="Green (555nm)" package="5 mm [THT]"]
  220_2 = Resistor [tolerance=±5% resistance=220 package=THT]
  SEND = LED - 5mm [color="Green (555nm)" package="5 mm [THT]"]
  220_3 = Resistor [tolerance=±5% resistance=220 package=THT]

nets:
  N1: Chiliduino-001.D6, SOIL_TEMPERATURE_SENSOR.pin1
  N2: Chiliduino-001.D5, AIR_TEMPERATURE_HUMIDITY_SENSOR.pin1
  N3: Chiliduino-001.D2, 220_3.Pin_1
  N4: Chiliduino-001.D1TX, 220_2.Pin_1
  N5: Chiliduino-001.D0RX, 220.Pin_1
  N6: Chiliduino-001.+5V, SOIL_MOISTURE_SENSOR.pin2, SOIL_TEMPERATURE_SENSOR.pin2, AIR_TEMPERATURE_HUMIDITY_SENSOR.pin2
  N7: Chiliduino-001.GND, SOIL_MOISTURE_SENSOR.pin3, SOIL_TEMPERATURE_SENSOR.pin3, AIR_TEMPERATURE_HUMIDITY_SENSOR.pin3, WIFI.cathode, READ.cathode, SEND.cathode
  N8: Chiliduino-001.A5, SOIL_MOISTURE_SENSOR.pin1
  N9: WIFI.anode, 220.Pin_0
  N10: READ.anode, 220_2.Pin_0
  N11: SEND.anode, 220_3.Pin_0
