# Fritzing sketch id105_317VCPreA154_0 (saved by Fritzing 0.8.7b)
circuit board: 4.02001cm x 23.1782cm
breadboards: 1

parts:
  +(-1 = DC025M-2.5-JL
  10k = Big Potentiometer [part_number=20k]
  LED5 = LED - 3mm [color="Red (633nm)" part_number=GL5516 package="3 mm [THT]"]
  LED6 = LED - 3mm [color="Red (633nm)" part_number=URed package="3 mm [THT]"]
  Q7 = DPAK1
  C9 = Electrolytic Capacitor [capacitance=1µF package="100 mil [THT, electrolytic]"]
  Q12 = sod-23-4
  P6 = Big Potentiometer [part_number=20k]
  P7 = Big Potentiometer [part_number=20k]
  P8 = Big Potentiometer [part_number=20k]
  RED = double row smd female pin header, 10 pins [form="♀ (female)"]
  2134 = SO08 [chip_label=IC package=SO]
  GL5537 = LED - 3mm [color="Red (633nm)" part_number=GL5537 package="3 mm [THT]"]
  URed = LED - 3mm [color="Red (633nm)" part_number=URed package="3 mm [THT]"]
  C1 = Ceramic Capacitor [capacitance=100nF package="1206 [SMD, multilayer]"]
  Q12_2 = sod-23-4
  Pad1 = Pad [width=14 height=9.2 connect=center]
  Pad2 = Pad [width=4 height=2.1 connect=center]
  Pad3 = Pad [width=4 height=2.1 connect=center]
  pj-301b18 = pj_301b2
  pj-301b20 = pj_301b2
  pj-301b21 = pj_301b2
  C1_2 = Ceramic Capacitor [capacitance=100nF package="1206 [SMD, multilayer]"]
  C16 = Ceramic Capacitor [capacitance=100nF package="1206 [SMD, multilayer]"]
  R130 = PTV09 [part_number=20k]
  104 = 0805 cap
  104_2 = 0805 cap
  100k = 0805-resistor [tolerance=±5%]
  100k_2 = 0805-resistor [tolerance=±5%]
  100k_3 = 0805-resistor [tolerance=±5%]
  D18 = sod-80-wide1 [part_number=1N4001]
  D8 = sod-80-wide1 [part_number=1N4001]
  317 = Pad [width=9.4 height=9.4 connect=center]  # not connected
  Preamplifier = Pad [width=9.4 height=9.4 connect=center]  # not connected
  100k? = 0805-resistor [tolerance=±5%]
  4148 = sod-80-wide1 [part_number=1N4001]
  D22 = sod-80-wide1 [part_number=1N4001]
  4k7? = 0805-resistor [tolerance=±5%]
  R132 = Resistor [tolerance=±5% resistance=220 package=THT]
  D17 = sod-80-wide1 [part_number=1N4001]
  C1_3 = Ceramic Capacitor [capacitance=100nF package="1206 [SMD, multilayer]"]
  104_3 = 0805-resistor [tolerance=±5%]
  C1_4 = Ceramic Capacitor [capacitance=100nF package="1206 [SMD, multilayer]"]
  Pad5 = Pad [width=8 height=2.4 connect=center]
  Pad6 = Pad [width=8 height=2.4 connect=center]
  D23 = sod-80-wide1 [part_number=1N4001]
  J18 = female pin header, 7 pins [form="♀ (female)"]
  J20 = female pin header, 7 pins [form="♀ (female)"]
  1k = MELF resistor CSR
  R3 = MELF resistor CSR
  R9 = MELF resistor CSR
  R1 = MELF resistor CSR
  1k_2 = MELF resistor CSR
  1k_3 = MELF resistor CSR
  R1_2 = MELF resistor CSR
  R4 = MELF resistor CSR
  R8 = MELF resistor CSR
  C1_5 = Ceramic Capacitor [capacitance=100nF package="1206 [SMD, multilayer]"]
  1k_4 = MELF resistor CSR
  C28 = Electrolytic Capacitor [capacitance=1µF package="100 mil [THT, electrolytic]"]
  red2 = LED - 3mm [color="Red (633nm)" part_number=Red package="3 mm [THT]"]
  R1_3 = MELF resistor CSR
  101 = 0805-resistor [tolerance=±5%]
  10k_2 = MELF resistor CSR
  104_4 = 0805-resistor [tolerance=±5%]
  Pad29 = Pad [width=4 height=1.2 connect=center]
  Part1 = Arduino Pro Mini v13  # not connected
  pj-301b24 = pj_301b2
  Pad12 = Pad [width=4 height=3.2 connect=center]
  D24 = sod-80-wide1 [part_number=1N4001]
  ?k = 0805 cap
  20k = 0805-resistor [tolerance=±5%]
  1k_5 = 0805-resistor [tolerance=±5%]
  1k_6 = 0805-resistor [tolerance=±5%]
  1m = 0805-resistor
  C1_6 = Ceramic Capacitor [capacitance=100nF package="1206 [SMD, multilayer]"]
  R4_2 = MELF resistor CSR
  R4_3 = MELF resistor CSR
  BAT = sod-23-4
  104_5 = 0805 cap
  1k_7 = MELF resistor CSR
  BAT_2 = sod-23-4
  Pad31 = Pad [width=2.2 height=4.6 connect=center]
  1k_8 = 0805-resistor [tolerance=±5%]
  3 = female pin header, 6 pins [form="♀ (female)"]
  101_2 = 0805 cap
  BAT_3 = sod-23-4
  10k? = MELF resistor CSR
  LED11 = LED - 3mm [color="Red (633nm)" part_number=Green package="3 mm [THT]"]
  1k_9 = 0805-resistor [tolerance=±5%]
  100k?1 = 0805-resistor [tolerance=±5%]
  161-3402-E = JC-204S
  10k_3 = 3362P
  1k_10 = 3362P_s
  D26 = sod-80-wide1 [part_number=1N4001]
  C1_7 = Ceramic Capacitor [capacitance=100nF package="1206 [SMD, multilayer]"]
  100k_4 = 0805-resistor [tolerance=±5%]
  R22 = 0805-resistor [tolerance=±5%]
  J21 = female pin header, 6 pins [form="♀ (female)"]
  Power = female pin header, 3 pins [form="♀ (female)"]
  A2 = female pin header, 2 pins [form="♀ (female)"]
  Raw = female pin header, 2 pins [form="♀ (female)"]
  gnd = female pin header, 2 pins [form="♀ (female)"]
  KS01-BL = KS01_LED

nets:
  N1: +(-1.connector1, C9.-, C1_2.0, D8.connector1, pj-301b24.connector2, D24.connector1, ?k.connector0, 104_5.connector0, 1k_10.connector0, Power.pin1, Power.pin3
  N2: +(-1.connector2, Pad3.pad, Power.pin2
  N3: 10k.connector0, 10k.connector1, P6.connector0, P6.connector1, P6.connector2, P7.connector0, P7.connector1, P7.connector2, P8.connector0, P8.connector1, P8.connector2, RED.pin2, RED.pin3, RED.pin4, RED.pin7, RED.pin8, RED.pin9, pj-301b18.connector1, pj-301b18.connector2, pj-301b18.connector3, pj-301b20.connector1, pj-301b20.connector2, pj-301b21.connector1, pj-301b21.connector2, R130.connector0, R130.connector3, R130.connector4, 104.connector0, 104_2.connector0, 4148.connector1, D22.connector0, 4k7?.connector0, 104_3.connector1, C1_4.1, 1k.connector1, R9.connector1, R1.connector0, 1k_3.connector0, R1_2.connector0, C1_5.1, 1k_4.connector0, C28.-, R1_3.connector1, 101.connector0, 10k_2.connector0, 104_4.connector0, 1k_6.connector1, R4_2.connector1, BAT.connector1, BAT_2.connector1, 101_2.connector0, BAT_3.connector1, LED11.cathode, 100k?1.connector1, 10k_3.connector2, C1_7.0, Raw.pin2, gnd.pin1, KS01-BL.connector2, KS01-BL.connector3, KS01-BL.connector5
  N4: 10k.connector2, R130.connector1, R130.connector2
  N5: 10k.connector3, 100k_3.connector0
  N6: 10k.connector4, Q12.connector2, P8.connector4, 2134.8, Q12_2.connector2, 104.connector1, R132.Pin_1, D17.connector0, 104_3.connector0, C1_5.0, C28.+, 104_4.connector1, Raw.pin1
  N7: LED5.cathode, Q7.connector1, Pad1.pad, Pad5.pad, Pad6.pad, D23.connector1, J18.pin1, J18.pin2, J18.pin3, J18.pin4, J18.pin5, J18.pin6, J18.pin7, J20.pin1, J20.pin2, J20.pin3, J20.pin4, J20.pin5, J20.pin6, J20.pin7, Pad29.pad, Pad12.pad, J21.pin1, J21.pin2, J21.pin3, J21.pin4, J21.pin5, J21.pin6
  N8: LED5.anode, Q7.connector0, 1k_7.connector1, Pad31.pad, D26.connector1
  N9: LED6.cathode, 1k.connector0
  N10: LED6.anode, Q12.connector0, 1k_9.connector0
  N11: Q7.connector2, C9.+, Pad2.pad, C1_2.1, D8.connector0, D23.connector0, D26.connector0
  N12: Q12.connector1, 100k_2.connector1, 100k_3.connector1, 20k.connector0
  N13: P6.connector3, 100k_2.connector0
  N14: P7.connector3, 2134.3, R1.connector1
  N15: P7.connector4, GL5537.anode, 1k_3.connector1
  N16: P8.connector3, 100k?.connector1, 4k7?.connector1
  N17: RED.pin1, RED.pin10, D18.connector0
  N18: RED.pin5, RED.pin6, D17.connector1
  N19: 2134.1, R3.connector0, R8.connector0
  N20: 2134.2, R8.connector1, 1k_4.connector1
  N21: 2134.4, 104_2.connector1, D18.connector1, C1_4.0
  N22: 2134.5, 4148.connector0, D22.connector1, 1k_2.connector0, 101.connector1
  N23: 2134.6, R9.connector0, R4.connector0
  N24: 2134.7, C16.1, R4.connector1
  N25: GL5537.cathode, C16.0
  N26: URed.cathode, 1k_6.connector0
  N27: URed.anode, Q12_2.connector0, red2.anode
  N28: C1.0, R3.connector1
  N29: C1.1, pj-301b21.connector0, R1_3.connector0
  N30: Q12_2.connector1, 100k.connector0, 100k?.connector0
  N31: pj-301b18.connector0, 10k?.connector0
  N32: pj-301b20.connector0, 100k.connector1
  N33: pj-301b20.connector3, R132.Pin_0
  N34: pj-301b21.connector3, 100k?1.connector0
  N35: C1_3.0, 1k_2.connector1, R1_2.connector1
  N36: C1_3.1, 161-3402-E.connector0
  N37: red2.cathode, 10k_2.connector1
  N38: pj-301b24.connector0, D24.connector0, ?k.connector1, 104_5.connector1
  N39: 20k.connector1, BAT_2.connector2, 3.pin2
  N40: 1k_5.connector0, BAT.connector2, 3.pin6, 100k_4.connector0
  N41: 1k_5.connector1, C1_6.0
  N42: 1m.connector0, 3.pin5, R22.connector1
  N43: 1m.connector1, 3.pin4
  N44: C1_6.1, 161-3402-E.connector1
  N45: R4_2.connector0, R4_3.connector1, C1_7.1, 100k_4.connector1, R22.connector0
  N46: R4_3.connector0, BAT.connector0, BAT_2.connector0, BAT_3.connector0, 10k_3.connector0, gnd.pin2
  N47: 1k_7.connector0, 1k_10.connector1, 1k_10.connector2
  N48: 1k_8.connector0, KS01-BL.connector6
  N49: 1k_8.connector1, 3.pin3
  N50: 3.pin1, KS01-BL.connector1
  N51: 101_2.connector1, BAT_3.connector2, 10k?.connector1, A2.pin1
  N52: LED11.anode, 1k_9.connector1
  N53: 10k_3.connector1, A2.pin2

notes:
  +
  RED
  -----------------------------------------------
  v-score
  GL5516
  ULed
  ]
