# Fritzing sketch id1060_chinotest_0 (saved by Fritzing 0.8.5b)
breadboards: 1

parts:
  Part1 = Arduino Nano (Rev3.0)
  DS2 = DS18B20 1-Wire Temperature Sensor [part_number=DS18B20]
  R1 = Resistor [tolerance=±5% resistance=4.7k package=THT]
  VCC1 = Battery block 9V
  JP1 = Header 2 [package=springterminal-2.54mm-2]

nets:
  GND: Part1.GND, DS2.GND, VCC1.-, JP1.1
  N1: Part1.D2, JP1.2
  N2: Part1.D10, DS2.DQ, R1.Pin_1
  N3: Part1.VIN, VCC1.+
  5V: Part1.5V, DS2.VDD, R1.Pin_0
