# Fritzing sketch id1062_Check_color_0 (saved by Fritzing 0.9.3b)
circuit board: 8.46667cm x 5.64444cm
breadboards: 1

parts:
  Composant1 = Arduino Uno (Rev3)
  LED1 = RGB LED (com. cathode, rgb) [package="5 mm [THT]"]
  R1 = Resistor [tolerance=±5% resistance=10k package=THT]
  R2 = Resistor [tolerance=±5% resistance=10k package=THT]
  R3 = Resistor [tolerance=±5% resistance=220 package=THT]
  R4 = Resistor [tolerance=±5% resistance=220 package=THT]
  R5 = Resistor [tolerance=±5% resistance=220 package=THT]
  S1 = Pushbutton [package="[THT]"]
  S2 = Pushbutton [package="[THT]"]

nets:
  N1: Composant1.GND, LED1.common_cathode, R1.Pin_0, R2.Pin_0
  N2: Composant1.D3_PWM, R1.Pin_1, S1.Pin_3, S1.Pin_4
  N3: Composant1.D4, R4.Pin_0
  N4: Composant1.D5_PWM, R3.Pin_0
  N5: Composant1.D6_PWM, R5.Pin_0
  N6: Composant1.D7, R2.Pin_1, S2.Pin_3, S2.Pin_4
  N7: Composant1.5V, S1.Pin_1, S1.Pin_2, S2.Pin_1, S2.Pin_2
  N8: LED1.red_anode, R5.Pin_1
  N9: LED1.green_anode, R3.Pin_1
  N10: LED1.blue_anode, R4.Pin_1
