# Fritzing sketch id1065_CIRC_09_Photoresistor_0 (saved by Fritzing 0.8.3b)
breadboards: 1

parts:
  Part1 = Arduino Uno (Rev3)
  R1 = Resistor [tolerance=±5% resistance=560 package=THT]
  LED1 = LED - 5mm [color="Red (633nm)" package="5 mm [THT]"]  # not connected
  R2 = Resistor [tolerance=±5% resistance=220 package=THT]
  R3 = PHOTOCELL [package=photocell-kit]

nets:
  N1: Part1.A0, R2.Pin_0, R3.P$2
  N2: Part1.5V, R1.Pin_1, R2.Pin_1
  N3: Part1.GND, R3.P$1
