# Fritzing sketch id1066_CBF_0 (saved by Fritzing 0.9.2b)

parts:
  S1 = SWITCH-SPST-2 [package=switch-spst-vertical]
  K1 = RELAY-2 [package=relay-g5v]
  SG1 = Buzzer 12mm [package=buzzer-ccv-kit]
  B1 = Battery block 9V

nets:
  N1: S1.O, SG1.1
  N2: S1.P, K1.1
  N3: K1.6, B1.+
  N4: SG1.2, B1.-
