# Fritzing sketch id1068_Untitled_Sketch_2_0 (saved by Fritzing 0.8.7b)
breadboards: 1

parts:
  Part1 = Arduino Uno (Rev3)
  LED1 = LED - 5mm [color="Red (633nm)" package="5 mm [THT]"]
  LED2 = LED - 5mm [color="Yellow (595nm)" package="5 mm [THT]"]
  LED3 = LED - 5mm [color="Green (555nm)" package="5 mm [THT]"]
  LED4 = LED - 5mm [color="Red (633nm)" package="5 mm [THT]"]
  LED5 = LED - 5mm [color="Yellow (595nm)" package="5 mm [THT]"]
  LED6 = LED - 5mm [color="Green (555nm)" package="5 mm [THT]"]
  R1 = Resistor [tolerance=±5% resistance=220 package=THT]
  R2 = Resistor [tolerance=±5% resistance=220 package=THT]
  R3 = Resistor [tolerance=±5% resistance=220 package=THT]
  R4 = Resistor [tolerance=±5% resistance=220 package=THT]
  R6 = Resistor [tolerance=±5% resistance=220 package=THT]
  R7 = Resistor [tolerance=±5% resistance=220 package=THT]

nets:
  N1: Part1.D2, LED6.anode
  N2: Part1.D3_PWM, LED5.anode
  N3: Part1.D4, LED4.anode
  N4: Part1.D5_PWM, LED3.anode
  N5: Part1.D6_PWM, LED2.anode
  N6: Part1.D7, LED1.anode
  N7: Part1.GND, R1.Pin_1, R2.Pin_1, R3.Pin_1, R4.Pin_1, R6.Pin_0, R7.Pin_0
  N8: LED1.cathode, R6.Pin_1
  N9: LED2.cathode, R7.Pin_1
  N10: LED3.cathode, R4.Pin_0
  N11: LED4.cathode, R3.Pin_0
  N12: LED5.cathode, R2.Pin_0
  N13: LED6.cathode, R1.Pin_0
