# Fritzing sketch id1069_Untitled_Sketch_3_0 (saved by Fritzing 0.9.2b)
breadboards: 1

parts:
  R1 = Resistor [tolerance=±5% resistance=470 package=THT]
  S1 = Pushbutton [package="[THT]"]
  R3 = Resistor [tolerance=±5% resistance=220 package=THT]
  VCC1 = Battery
  LED1 = LED - 5mm [color="Red (633nm)" package="5 mm [THT]"]
  LED2 = LED - 5mm [color="Red (633nm)" package="5 mm [THT]"]

nets:
  N1: R1.Pin_0, S1.Pin_1, S1.Pin_2, R3.Pin_0
  N2: R1.Pin_1, LED1.cathode
  N3: S1.Pin_3, S1.Pin_4, VCC1.-
  N4: R3.Pin_1, LED2.cathode
  N5: VCC1.+, LED1.anode, LED2.anode
