# Fritzing sketch id106_32x32_led_matrix_pcb_rev4_0 (saved by Fritzing 0.8.7b)
circuit board: 5cm x 4.32cm
breadboards: 1

parts:
  Teensy_3_1 = Teensy 3.1
  D1 = Rectifier Diode [package="Melf DO-213 AA [SMD]"]
  MTX = double row female pin header, 16 pins [form="♀ (female)"]
  ++-_- = female pin header, 4 pins [form="♀ (female)"]
  +TX_RX- = female pin header, 4 pins [form="♀ (female)"]
  5v_in = Power Jack [package=power_jack_pth]
  SPKR = female pin header, 2 pins [form="♀ (female)"]
  C1 = Ceramic Capacitor [capacitance=10µF package="0603 [SMD, multilayer]"]
  +_- = female pin header, 2 pins [form="♀ (female)"]
  R1 = Resistor [tolerance=±5% resistance=1k package="0603 [SMD]"]
  R2 = Resistor [tolerance=±5% resistance=1k package="0603 [SMD]"]
  -_A10_A11_3V3_5V = female pin header, 5 pins [form="♀ (female)"]
  IR_I2C = female pin header, 7 pins [form="♀ (female)"]
  Pad1 = Pad [width=5 height=2.54 connect=center]
  Pad2 = Pad [width=5 height=2.54 connect=center]
  BAT = CR1220_JTRON
  MicroSD = Micro SD Ali

nets:
  GND: Teensy_3_1.GND, MTX.pin9, MTX.pin13, MTX.pin15, ++-_-.pin3, ++-_-.pin4, +TX_RX-.pin4, 5v_in.GND, 5v_in.GNDBREAK, SPKR.pin1, +_-.pin2, -_A10_A11_3V3_5V.pin1, IR_I2C.pin1, IR_I2C.pin4, Pad2.pad, BAT.connector2, MicroSD.connector0, MicroSD.connector2, MicroSD.connector4, MicroSD.connector5, MicroSD.connector9
  N1: Teensy_3_1.D0, +TX_RX-.pin3
  N2: Teensy_3_1.D1, +TX_RX-.pin2
  N3: Teensy_3_1.D2, MTX.pin1
  N4: Teensy_3_1.D3, Teensy_3_1.D8, MTX.pin10
  N5: Teensy_3_1.D4, MTX.pin8
  N6: Teensy_3_1.D5, MTX.pin16
  N7: Teensy_3_1.D6, MTX.pin2
  N8: Teensy_3_1.D7, MTX.pin14
  N9: Teensy_3_1.D9, MTX.pin5
  N10: Teensy_3_1.D10, MTX.pin12
  N11: Teensy_3_1.D11, MicroSD.connector6
  N12: Teensy_3_1.D12, MicroSD.connector10
  N13: Teensy_3_1.VBat, BAT.connector0
  N14: Teensy_3_1.A14/DAC, C1.1
  N15: Teensy_3_1.D13, MicroSD.connector8
  N16: Teensy_3_1.A0/D14, MTX.pin7
  N17: Teensy_3_1.A1/D15, MicroSD.connector3
  N18: Teensy_3_1.A3/D17, IR_I2C.pin2
  N19: Teensy_3_1.A4/D18, R2.Pin_0, IR_I2C.pin5
  N20: Teensy_3_1.A5/D19, R1.Pin_0, IR_I2C.pin6
  N21: Teensy_3_1.A6/D20, MTX.pin4
  N22: Teensy_3_1.A7/D21, MTX.pin3
  N23: Teensy_3_1.A8/D22, MTX.pin6
  N24: Teensy_3_1.A9/D23, MTX.pin11
  N25: Teensy_3_1.3V3, R1.Pin_1, R2.Pin_1, -_A10_A11_3V3_5V.pin4, MicroSD.connector7
  N26: Teensy_3_1.Vin, D1.cathode, +TX_RX-.pin1, -_A10_A11_3V3_5V.pin5, IR_I2C.pin3, IR_I2C.pin7
  N27: Teensy_3_1.A11, -_A10_A11_3V3_5V.pin3
  N28: Teensy_3_1.A10, -_A10_A11_3V3_5V.pin2
  N29: D1.anode, ++-_-.pin1, ++-_-.pin2, 5v_in.PWR, +_-.pin1, Pad1.pad
  N30: SPKR.pin2, C1.0

notes:
  By Kjetilei 2014
  board for Teensy 3.1
  RGB LED matrix
