# Fritzing sketch id1071_Butona (saved by Fritzing 0.9.3b)
breadboards: 1

parts:
  Parça1 = Arduino Uno (Rev3)
  Buton = Pushbutton [package="[THT]"]
  LED1 = LED - 3mm [color="Red (633nm)" package="3 mm [THT]"]
  R1 = Resistor [tolerance=±5% resistance=220 package=THT]
  Direnç = Resistor [tolerance=±5% resistance=220 package=THT]

nets:
  N1: Parça1.D12/MISO, Buton.Pin_1, Buton.Pin_2, Direnç.Pin_0
  N2: Parça1.D13/SCK, LED1.anode
  N3: Parça1.5V, Buton.Pin_3, Buton.Pin_4
  N4: Parça1.GND, R1.Pin_0, Direnç.Pin_1
  N5: LED1.cathode, R1.Pin_1
