# Fritzing sketch id1071_circuitoControleRodas_0 (saved by Fritzing 0.9.2b)
perfboards: 1

parts:
  D1 = Rectifier Diode [part_number=1N4001 package="300 mil [THT]"]
  D2 = Rectifier Diode [part_number=1N4001 package="300 mil [THT]"]
  D3 = Rectifier Diode [part_number=1N4001 package="300 mil [THT]"]
  D4 = Rectifier Diode [part_number=1N4001 package="300 mil [THT]"]
  D5 = Rectifier Diode [part_number=1N4001 package="300 mil [THT]"]
  D6 = Rectifier Diode [part_number=1N4001 package="300 mil [THT]"]
  D7 = Rectifier Diode [part_number=1N4001 package="300 mil [THT]"]
  D8 = Rectifier Diode [part_number=1N4001 package="300 mil [THT]"]
  IC2 = Arduino Nano (Rev3.0)
  IC1 = L293D [package=THT]
  M2 = Screw terminal - 2 pins [package=THT]
  J2 = Screw terminal - 2 pins [package=THT]
  J3 = Screw terminal - 2 pins [package=THT]

nets:
  N1: D1.cathode, D4.anode, IC1.Out_1_(_Controlled_by_Enable_1_), J3.pin2
  GND: D1.anode, D2.anode, D5.anode, D8.anode, IC2.GND, IC1.0V, J2.pin2
  N2: D2.cathode, D3.anode, IC1.Out_2_(_Controlled_by_Enable_1_), J3.pin1
  N3: D3.cathode, D4.cathode, D6.cathode, D7.cathode, IC1.+Vmotor, J2.pin1
  N4: D5.cathode, D6.anode, IC1.Out_4_(_Controlled_by_Enable_2_), M2.pin1
  N5: D7.anode, D8.cathode, IC1.Out_3_(_Controlled_by_Enable_2_), M2.pin2
  N6: IC2.D7, IC1.In_2
  N7: IC2.D8, IC1.In_1
  N8: IC2.D9, IC1.Enable_1
  N9: IC2.D10, IC1.Enable_2
  N10: IC2.D11/MOSI, IC1.In_3
  N11: IC2.D12/MISO, IC1.In_4
  N12: IC2.5V, IC1.+V
