# Fritzing sketch id1072_Workshop_01_Blink_0 (saved by Fritzing 0.9.0b)

parts:
  Bauteil1 = Arduino Uno (Rev3)
  LED1 = LED - 5mm [color="Red (633nm)" package="5 mm [THT]"]

nets:
  N1: Bauteil1.D13/SCK, LED1.anode
  N2: Bauteil1.GND, LED1.cathode

notes:
  FLIP FLOP
