# Fritzing sketch id1073_Untitled_Sketch_0 (saved by Fritzing 0.9.3b)
breadboards: 1

parts:
  VCC1 = Battery
  S1 = Pushbutton [package="[THT]"]  # not connected
  LED1 = LED - 5mm [color="Red (633nm)" package="5 mm [THT]"]
  LED2 = LED - 5mm [color="Red (633nm)" package="5 mm [THT]"]
  LED3 = LED - 5mm [color="Red (633nm)" package="5 mm [THT]"]
  LED4 = LED - 5mm [color="Red (633nm)" package="5 mm [THT]"]

nets:
  N1: VCC1.+, LED1.anode, LED2.anode, LED3.anode, LED4.anode
  N2: LED1.cathode, LED2.cathode, LED3.cathode, LED4.cathode
