# Fritzing sketch id1074_Untitled_Sketch_0 (saved by Fritzing 0.9.3b)
breadboards: 1

parts:
  Componente1 = Arduino Leonardo (Rev3b)
  LED1 = LED - 3mm [color="Red (633nm)" package="3 mm [THT]"]
  LED2 = LED - 3mm [color="Red (633nm)" package="3 mm [THT]"]
  LED4 = LED - 3mm [color="Orange (612nm)" package="3 mm [THT]"]
  R2 = Resistor [tolerance=±5% resistance=220 package=THT]
  R3 = Resistor [tolerance=±5% resistance=220 package=THT]  # not connected
  R4 = Resistor [tolerance=±5% resistance=220 package=THT]
  R5 = Resistor [tolerance=±5% resistance=220 package=THT]
  R6 = Resistor [tolerance=±5% resistance=220 package=THT]
  LED3 = RGB LED (6 legs) [color="Red (633nm)" package="5 mm [THT]"]  # not connected

nets:
  N1: Componente1.D5_PWM, LED1.cathode, LED2.cathode, LED4.cathode, R2.Pin_0, R4.Pin_0, R6.Pin_0
  N2: Componente1.GND, R2.Pin_1, R4.Pin_1, R5.Pin_1, R6.Pin_1
  N3: LED1.anode, R5.Pin_0
