# Fritzing sketch id1075_CKP_SIMULATOR_0 (saved by Fritzing 0.9.3b)
breadboards: 1

parts:
  U1 = 555 Timer [package="DIP8 [THT]"]
  R1 = Resistor [tolerance=±5% resistance=220 package=THT]
  R2 = Trimmer Potentiometer [maximum_resistance=10kΩ package=THT]  # not connected
  C1 = Ceramic Capacitor [capacitance=100nF package="100 mil [THT, multilayer]"]
  C2 = Electrolytic Capacitor [capacitance=1µF package="100 mil [THT, electrolytic]"]
  R3 = Resistor [tolerance=±5% resistance=220 package=THT]
  LED1 = LED - 5mm [color="Red (633nm)" package="5 mm [THT]"]

nets:
  N1: U1.Ground, C1.1, C2.-, LED1.cathode
  N2: U1.Trigger, C2.+
  N3: U1.Output, R3.Pin_0
  N4: U1.Control_Voltage, C1.0
  N5: U1.Discharge, R1.Pin_0
  N6: U1.Vcc_Supply_Voltage, R1.Pin_1
  N7: R3.Pin_1, LED1.anode
