# Fritzing sketch id1076_Untitled_Sketch_0 (saved by Fritzing 0.9.3b)
breadboards: 1

parts:
  Q1 = PNP-Transistor [package="TO92 [THT]"]
  R1 = Resistor [tolerance=±5% resistance=220 package=THT]
  Q2 = PNP-Transistor [package="TO92 [THT]"]
  LED1 = LED - 5mm [color="Red (633nm)" package="5 mm [THT]"]
  R2 = Resistor [tolerance=±5% resistance=220 package=THT]
  FLAMA = Hirose DF13 Series Header [part_number=DF13A-2P-1.25H package=DF13A-2P-1.25H]  # not connected
  9V = Battery block 9V

nets:
  N1: Q1.E, Q2.B
  N2: Q1.C, R1.Pin_1
  N3: Q2.E, 9V.-
  N4: Q2.C, LED1.cathode
  N5: LED1.anode, R2.Pin_1
  N6: R2.Pin_0, 9V.+
