# Fritzing sketch id1077_clavero_en_movimiento_LCD__0 (saved by Fritzing 0.9.2b)
breadboards: 1

parts:
  Parte1 = Arduino Uno (Rev3)
  RE3 = Rotary Encoder [package=THT]
  LCD1 = LCD screen

nets:
  N1: Parte1.D11_PWM/MOSI, LCD1.E
  N2: Parte1.D12/MISO, LCD1.RS
  N3: Parte1.D2, LCD1.DB7
  N4: Parte1.D3_PWM, LCD1.DB6
  N5: Parte1.D4, LCD1.DB5
  N6: Parte1.D5_PWM, LCD1.DB4
  5V: Parte1.5V, RE3.EncoderPinB, LCD1.VDD, LCD1.LED+
  GND: Parte1.GND, RE3.EncoderPinA, LCD1.VSS, LCD1.R/W, LCD1.LED-
  N7: RE3.EncoderPinC, LCD1.V0
