# Fritzing sketch id1079_Asteroid_Mine_0 (saved by Fritzing 0.9.3b)
breadboards: 3

parts:
  Part1 = Arduino Mega ADK (Rev3)
  S1 = Round Pushbutton
  LED1 = smd LED [color="Red (633nm)" package="0805 [SMD]"]
  S2 = Round Pushbutton
  LED2 = smd LED [color="Red (633nm)" package="0805 [SMD]"]
  S3 = Round Pushbutton
  LED3 = smd LED [color="Red (633nm)" package="0805 [SMD]"]
  S4 = Round Pushbutton
  S5 = Round Pushbutton
  LED5 = smd LED [color="Red (633nm)" package="0805 [SMD]"]
  LED6 = smd LED [color="Red (633nm)" package="0805 [SMD]"]
  S6 = Round Pushbutton
  S7 = Round Pushbutton
  S8 = Round Pushbutton
  S9 = Round Pushbutton
  S10 = Round Pushbutton
  M1 = Stepper Motor - Bipolar  # not connected
  M2 = Stepper Motor - Bipolar  # not connected
  M3 = Stepper Motor - Bipolar  # not connected
  M4 = Stepper Motor - Bipolar  # not connected
  M5 = Stepper Motor - Bipolar  # not connected

nets:
  N1: Part1.D20/SDA, S5.leg1
  N2: Part1.D19/RX1, LED5.anode
  N3: Part1.D17/RX2, S6.leg0
  N4: Part1.D16/TX2, S7.leg0
  N5: Part1.D15/RX3, S8.leg0
  N6: Part1.D14/TX3, S9.leg0
  N7: Part1.D13_PWM, LED1.anode
  N8: Part1.D12_PWM, S1.leg1
  N9: Part1.D10_PWM, S2.leg1
  N10: Part1.D9_PWM, LED2.anode
  N11: Part1.D8_PWM, S3.leg1
  N12: Part1.GND, S1.leg0, LED1.cathode, S2.leg0, LED2.cathode, S3.leg0, LED3.cathode, S4.leg0, S5.leg0, LED5.cathode, LED6.cathode
  N13: Part1.D6_PWM, LED3.anode
  N14: Part1.D22, LED6.anode
  N15: Part1.D23, S4.leg1
  N16: Part1.D25, S10.leg0

notes:
  X+
  Y+
  X-
  Y-
  Red
  To DC Power
  X_Low_Limit
  X_High_Limit
  Y_Low_Limit
  Y_High_Limit
  A_Limit
  X1
  X2
  Y
  Z
  CLAW
  X1 MOTOR DRIVER
  X2 MOTOR DRIVER
  Y MOTOR DRIVER
  Z MOTOR DRIVER
  A MOTOR DRIVER
