# Fritzing sketch id107_3D_Printer_0 (saved by Fritzing 0.9.3b)
circuit board: 8.93992cm x 8.51126cm
breadboards: 1

parts:
  Arduino = Arduino Nano (Rev3.0)
  Z_axis = Pololu A4988 [package=SO16]
  Y_axis = Pololu A4988 [package=SO16]
  X_axis = Pololu A4988 [package=SO16]
  part = Header 2 [package=screwterminal-3.5mm-2_lock]
  stepper = Header 1 [package=1x01_offset]
  part_2 = Header 1 [package=1x01_offset]
  part_3 = Header 1 [package=1x01_offset]
  part_4 = Header 1 [package=1x01_offset]
  part_5 = Header 1 [package=1x01_offset]
  part_6 = Header 1 [package=1x01_offset]
  part_7 = Header 1 [package=1x01_offset]
  stepper_2 = Header 1 [package=1x01_offset]
  stepper_3 = Header 1 [package=1x01_offset]
  part_8 = Header 1 [package=1x01_offset]
  part_9 = Header 1 [package=1x01_offset]
  part_10 = Header 1 [package=1x01_offset]
  light = Header 1 [package=1x01_offset]
  part_11 = Header 1 [package=1x01_offset]
  Spindle_Enable = Header 1 [package=1x01_offset]
  Stepper_Enable/Disable = Header 1 [package=1x01_offset]
  Spindle_Direction = Header 1 [package=1x01_offset]
  C1 = Electrolytic Capacitor [capacitance=47µF voltage=10V package="100 mil [THT, electrolytic]"]
  Coolant = Header 1 [package=1x01_offset]
  g = Header 1 [package=1x01_offset]
  Feed/Hold = Header 1 [package=1x01_offset]

nets (from the pcb view):
  N1: Arduino.GND, Z_axis.GND#8, X_axis.STEP
  N2: Arduino.D2, Y_axis.STEP
  N3: Arduino.D4, Z_axis.STEP
  N4: Arduino.D5, X_axis.DIR
  N5: Arduino.D6, Y_axis.DIR
  N6: Arduino.D7, Z_axis.DIR
  N7: Arduino.D8, Stepper_Enable/Disable.1
  N8: Arduino.D12/MISO, Spindle_Enable.1
  N9: Arduino.5V, part_11.1
  N10: Arduino.A3, Coolant.1
  N11: Arduino.A1, Feed/Hold.1
  N12: Arduino.D13/SCK, Spindle_Direction.1
  N13: Z_axis.1B, part_5.1
  N14: Z_axis.1A, part_6.1
  N15: Z_axis.2A, part_7.1
  N16: Z_axis.2B, stepper_2.1
  GND: Z_axis.GND#14, Y_axis.GND, X_axis.GND, part.1, C1.-
  N17: Z_axis.VMOT, Y_axis.VMOT, X_axis.VMOT, part.2, C1.+
  N18: Y_axis.1B, part_2.1
  N19: Y_axis.1A, part_3.1
  N20: Y_axis.2A, part_4.1
  N21: Y_axis.2B, stepper.1
  N22: X_axis.1B, part_10.1
  N23: X_axis.1A, part_9.1
  N24: X_axis.2A, part_8.1
  N25: X_axis.2B, stepper_3.1
  N26: light.1, g.1

notes:
  Made By Ahmed Mohiuddin Shah
  ©
