# Fritzing sketch id1080_Clock_0 (saved by Fritzing 0.7.4b)
breadboards: 1

parts:
  IC1 = IC, DIP package, 20 pins [chip_label="PICAXE 20M2" spacing=300mil]
  IC2 = IC, DIP package, 24 pins [chip_label="SAA 1064" spacing=600mil]
  9V_In = Power plug
  R1 = mystery part, 3 pins [chip_label=78L05 spacing=300mil]
  C1 = Ceramic Capacitor [capacitance=100nF package="100 mil [THT, multilayer]"]
  C2 = Electrolytic Capacitor [capacitance=0.1mF package="100 mil [THT, electrolytic]"]
  C3 = Electrolytic Capacitor [capacitance=0.47mF package="100 mil [THT, electrolytic]"]
  C4 = Ceramic Capacitor [capacitance=3.3pF package="100 mil [THT, multilayer]"]
  C5 = Ceramic Capacitor [capacitance=100nF package="100 mil [THT, multilayer]"]
  C6 = Ceramic Capacitor [capacitance=100nF package="100 mil [THT, multilayer]"]
  IC3 = IC, DIP package, 18 pins [chip_label=ULN2803A spacing=300mil]
  7_Segment1 = 7 Segment Display
  7_Segment2 = 7 Segment Display
  7_Segment3 = 7 Segment Display
  7_Segment4 = 7 Segment Display
  Q1 = PNP-Transistor [package="TO92 [THT]"]
  Q2 = PNP-Transistor [package="TO92 [THT]"]
  R2 = Resistor [tolerance=±5% resistance=510 package=THT]
  R3 = Resistor [tolerance=±5% resistance=510 package=THT]
  C7 = Ceramic Capacitor [capacitance=100nF package="100 mil [THT, multilayer]"]
  Chime1 = Screw terminal - 2 pins [package=THT]
  Chime2 = Screw terminal - 2 pins [package=THT]
  Chime3 = Screw terminal - 2 pins [package=THT]
  Chime4 = Screw terminal - 2 pins [package=THT]
  Chime5 = Screw terminal - 2 pins [package=THT]
  LED1 = LED - 5mm [color="Blue (430nm)" package="5 mm [THT]"]
  LED2 = LED - 5mm [color="Blue (430nm)" package="5 mm [THT]"]
  LED3 = LED - 5mm [color="Blue (430nm)" package="5 mm [THT]"]
  LED4 = LED - 5mm [color="Blue (430nm)" package="5 mm [THT]"]
  LED5 = LED - 5mm [color="Blue (430nm)" package="5 mm [THT]"]
  LED6 = LED - 5mm [color="Blue (430nm)" package="5 mm [THT]"]
  LED7 = LED - 5mm [color="Blue (430nm)" package="5 mm [THT]"]
  LED8 = LED - 5mm [color="Blue (430nm)" package="5 mm [THT]"]
  LED9 = LED - 5mm [color="Blue (430nm)" package="5 mm [THT]"]
  LED10 = LED - 5mm [color="Blue (430nm)" package="5 mm [THT]"]
  LED11 = LED - 5mm [color="Blue (430nm)" package="5 mm [THT]"]
  LED12 = LED - 5mm [color="Blue (430nm)" package="5 mm [THT]"]
  LED13 = LED - 5mm [color="Blue (430nm)" package="5 mm [THT]"]
  LED14 = LED - 5mm [color="Blue (430nm)" package="5 mm [THT]"]
  LED15 = LED - 5mm [color="Blue (430nm)" package="5 mm [THT]"]
  LED16 = LED - 5mm [color="Blue (430nm)" package="5 mm [THT]"]
  LED17 = LED - 5mm [color="Blue (430nm)" package="5 mm [THT]"]
  LED18 = LED - 5mm [color="Blue (430nm)" package="5 mm [THT]"]
  LED19 = LED - 5mm [color="Blue (430nm)" package="5 mm [THT]"]
  LED20 = LED - 5mm [color="Blue (430nm)" package="5 mm [THT]"]
  R4 = Resistor [tolerance=±5% resistance=47 package=THT]
  R5 = Resistor [tolerance=±5% resistance=47 package=THT]
  R6 = Resistor [tolerance=±5% resistance=47 package=THT]
  R7 = Resistor [tolerance=±5% resistance=47 package=THT]
  R8 = Resistor [tolerance=±5% resistance=47 package=THT]
  TRS1 = Stereo Jack (TRS) 3.5mm [package="PG203J [THT]"]
  R9 = Resistor [tolerance=±5% resistance=22k package=THT]
  R10 = Resistor [tolerance=±5% resistance=10k package=THT]
  R11 = Photocell (LDR) [package=THT]
  R12 = Resistor [tolerance=±5% resistance=10k package=THT]
  J6 = Piezo Speaker
  Doorbell = Screw terminal - 2 pins [package=THT]
  R13 = Resistor [tolerance=±5% resistance=10k package=THT]
  RevEd_IR_Sensor = mystery part, 3 pins [chip_label=IR spacing=300mil]
  R14 = Resistor [tolerance=±5% resistance=4.7k package=THT]
  C8 = Electrolytic Capacitor [capacitance=4.7µF package="100 mil [THT, electrolytic]"]
  Jungletronics_RTC = mystery part, 5 pins [chip_label=RTC spacing=300mil]
  R15 = Resistor [tolerance=±5% resistance=2.2k package=THT]
  R16 = Resistor [tolerance=±5% resistance=2.2k package=THT]

nets:
  5V: IC1.pin1, R1.pin1, C1.1, C2.+, C6.0, R11.pin_0, R13.Pin_1, RevEd_IR_Sensor.pin3, R14.Pin_0, C8.+, Jungletronics_RTC.pin5, R15.Pin_0, R16.Pin_0
  N1: IC1.pin2, R9.Pin_1
  N2: IC1.pin3, J6.pin2
  N3: IC1.pin4, Doorbell.pin1
  N4: IC1.pin5, RevEd_IR_Sensor.pin1, R14.Pin_1
  N5: IC1.pin6, IC3.pin5
  N6: IC1.pin7, IC3.pin4
  N7: IC1.pin8, IC3.pin3
  N8: IC1.pin9, IC3.pin2
  N9: IC1.pin10, IC3.pin1
  N10: IC1.pin11, IC2.pin24, Jungletronics_RTC.pin2, R16.Pin_1
  N11: IC1.pin12, R11.pin_1, R12.Pin_0
  N12: IC1.pin13, IC2.pin23, Jungletronics_RTC.pin1, R15.Pin_1
  N13: IC1.pin14, R8.Pin_1
  N14: IC1.pin15, R7.Pin_1
  N15: IC1.pin16, R6.Pin_1
  N16: IC1.pin17, R5.Pin_1
  N17: IC1.pin18, R4.Pin_1
  N18: IC1.pin19, TRS1.Ring
  GND: IC1.pin20, IC2.pin1, IC2.pin12, 9V_In.VCC, R1.pin2, C1.0, C2.-, C3.-, C4.0, C5.0, C6.1, IC3.pin9, C7.0, TRS1.Sleeve, R10.Pin_0, R12.Pin_1, J6.pin1, RevEd_IR_Sensor.pin2, C8.-, Jungletronics_RTC.pin4
  N19: IC2.pin2, C4.1
  N20: IC2.pin3, 7_Segment1.Segment_A, 7_Segment2.Segment_A
  N21: IC2.pin4, 7_Segment1.Segment_B, 7_Segment2.Segment_B
  N22: IC2.pin5, 7_Segment1.Segment_C, 7_Segment2.Segment_C
  N23: IC2.pin6, 7_Segment1.Segment_D, 7_Segment2.Segment_D
  N24: IC2.pin7, 7_Segment1.Segment_E, 7_Segment2.Segment_E
  N25: IC2.pin8, 7_Segment1.Segment_F, 7_Segment2.Segment_F
  N26: IC2.pin9, 7_Segment1.Segment_G, 7_Segment2.Segment_G
  N27: IC2.pin10, 7_Segment1.Segment_DP, 7_Segment2.Segment_DP
  N28: IC2.pin11, IC3.pin7
  9V: IC2.pin13, 9V_In.GND, R1.pin3, C3.+, C5.1, IC3.pin10, Q1.E, Q2.E, C7.1, Chime1.pin2, Chime2.pin2, Chime3.pin2, Chime4.pin2, Chime5.pin2
  N29: IC2.pin14, IC3.pin6
  N30: IC2.pin15, 7_Segment3.Segment_DP, 7_Segment4.Segment_DP
  N31: IC2.pin16, 7_Segment3.Segment_G, 7_Segment4.Segment_G
  N32: IC2.pin17, 7_Segment3.Segment_F, 7_Segment4.Segment_F
  N33: IC2.pin18, 7_Segment3.Segment_E, 7_Segment4.Segment_E
  N34: IC2.pin19, 7_Segment3.Segment_D, 7_Segment4.Segment_D
  N35: IC2.pin20, 7_Segment3.Segment_C, 7_Segment4.Segment_C
  N36: IC2.pin21, 7_Segment3.Segment_B, 7_Segment4.Segment_B
  N37: IC2.pin22, 7_Segment3.Segment_A, 7_Segment4.Segment_A
  N38: IC3.pin12, R2.Pin_1
  N39: IC3.pin13, R3.Pin_1
  N40: IC3.pin14, Chime5.pin1
  N41: IC3.pin15, Chime4.pin1
  N42: IC3.pin16, Chime3.pin1
  N43: IC3.pin17, Chime2.pin1
  N44: IC3.pin18, Chime1.pin1
  N45: 7_Segment1.common_anode, 7_Segment4.common_anode, Q2.C
  N46: 7_Segment2.common_anode, 7_Segment3.common_anode, Q1.C
  N47: Q1.B, R2.Pin_0
  N48: Q2.B, R3.Pin_0
  N49: LED1.cathode, LED5.anode, LED6.anode, LED7.anode, LED8.anode, LED10.cathode, LED14.cathode, LED18.cathode, R5.Pin_0
  N50: LED1.anode, LED2.anode, LED3.anode, LED4.anode, LED5.cathode, LED9.cathode, LED13.cathode, LED17.cathode, R4.Pin_0
  N51: LED2.cathode, LED6.cathode, LED9.anode, LED10.anode, LED11.anode, LED12.anode, LED15.cathode, LED19.cathode, R6.Pin_0
  N52: LED3.cathode, LED7.cathode, LED11.cathode, LED13.anode, LED14.anode, LED15.anode, LED16.anode, LED20.cathode, R7.Pin_0
  N53: LED4.cathode, LED8.cathode, LED12.cathode, LED16.cathode, LED17.anode, LED18.anode, LED19.anode, LED20.anode, R8.Pin_0
  N54: TRS1.Tip, R9.Pin_0, R10.Pin_1
  N55: Doorbell.pin2, R13.Pin_0
