# Fritzing sketch id1081_clonpi_0 (saved by Fritzing 0.8.7b)
breadboards: 1

parts:
  Raspberry_Pi_B_rev1 = Raspberry Pi B rev2
  LCD1 = LCD screen
  R1 = Resistor [tolerance=±5% resistance=560 package="0805 [SMD]"]
  R2 = Trimmer Potentiometer [maximum_resistance=10kΩ package=THT]

nets:
  5V: Raspberry_Pi_B_rev1.5V, LCD1.VDD, R1.Pin_0, R2.leg2
  GND: Raspberry_Pi_B_rev1.GND, Raspberry_Pi_B_rev1.GPIO_14, LCD1.VSS, LCD1.R/W, LCD1.LED-, R2.leg1
  N1: Raspberry_Pi_B_rev1.GPIO_23, LCD1.DB6
  N2: Raspberry_Pi_B_rev1.GPIO_18, LCD1.DB7
  N3: Raspberry_Pi_B_rev1.GPIO_24, LCD1.DB5
  N4: Raspberry_Pi_B_rev1.GPIO_25, LCD1.DB4
  N5: LCD1.V0, R2.wiper
  N6: LCD1.LED+, R1.Pin_1
