# Fritzing sketch id1082_ClothesPinLightAndSound_0 (saved by Fritzing 0.9.2b)
breadboards: 1

parts:
  R1 = Resistor [tolerance=±5% resistance=10 package=THT]
  J1 = Piezo Speaker
  Part1 = Arduino Uno (Rev3)
  LED1 = LED - 5mm [color="Red (633nm)" package="5 mm [THT]"]

nets:
  N1: R1.Pin_0, J1.pin1, Part1.GND, LED1.cathode
  N2: R1.Pin_1, Part1.D2
  N3: J1.pin2, Part1.D8
  N4: Part1.D13/SCK, LED1.anode

notes:
  Clothes Pin Key
