# Fritzing sketch id1083_Clyde+AdafruitCC3000_0 (saved by Fritzing 0.9.0b)
circuit board: 22.4757cm x 12.0725cm
breadboards: 1

parts:
  Fabule_Clyde = Arduino Leonardo (Rev3b)
  Adafruit_CC3000_WiFi_Shield = Arduino Prototyping Shield

nets:
  N1: Fabule_Clyde.D3_PWM/SCL, Fabule_Clyde.SCL, Adafruit_CC3000_WiFi_Shield.D3
  N2: Fabule_Clyde.D4/A6, Adafruit_CC3000_WiFi_Shield.D5
  5V: Fabule_Clyde.5V, Adafruit_CC3000_WiFi_Shield.+5V
  GND: Fabule_Clyde.GND, Adafruit_CC3000_WiFi_Shield.GND
  N3: Fabule_Clyde.D10_PWM/A10, Adafruit_CC3000_WiFi_Shield.D10
