# Fritzing sketch id1085_diagram_0 (saved by Fritzing 0.9.0b)

parts:
  Part1 = EasyDriver_v44
  Part2 = EasyDriver_v44
  Part3 = EasyDriver_v44
  M2 = Stepper Motor - Bipolar
  M3 = Stepper Motor - Bipolar
  J1 = ATX24 Pin Power Supply Connector [package=atx24_right_angle]
  Part4 = Arduino Uno (Rev3)
  M1 = Stepper Motor - Bipolar
  proto1 = Adafruit_PermaProto_1_4_Board

nets:
  GND: Part1.GND, Part2.GND, Part3.GND, Part4.GND, proto1.connectorZ1, proto1.connectorZ3, proto1.connectorZ13
  N1: Part1.V+, proto1.connectorY2
  N2: Part1.STEP, Part4.D4
  N3: Part1.DIR, Part4.D7
  N4: Part1.OUT2A, M1.A
  N5: Part1.OUT2B, M1.C
  N6: Part1.OUT1A, M1.B
  N7: Part1.OUT1B, M1.D
  N8: Part2.V+, proto1.connectorY4
  N9: Part2.STEP, Part4.D3_PWM
  N10: Part2.DIR, Part4.D6_PWM
  N11: Part2.OUT2A, M2.A
  N12: Part2.OUT2B, M2.C
  N13: Part2.OUT1A, M2.B
  N14: Part2.OUT1B, M2.D
  N15: Part3.V+, proto1.connectorY14
  N16: Part3.STEP, Part4.D2
  N17: Part3.DIR, Part4.D5_PWM
  N18: Part3.OUT2A, M3.A
  N19: Part3.OUT2B, M3.C
  N20: Part3.OUT1A, M3.B
  N21: Part3.OUT1B, M3.D
  N22: J1.GND, proto1.connectorZ15
  N23: J1.5V, proto1.connectorY15
