# Fritzing sketch id1086_cnc_flatbed_pen_plotter_schematic_0 (saved by Fritzing 0.9.3b)
breadboards: 1

parts:
  Часть1 = Arduino Uno (Rev3)
  Driver_PCB_X1 = ULN2003A [package="SO16 [SMD]"]
  X1 = Stepper Motor - Unipolar
  Driver_PCB_X2 = ULN2003A [package="SO16 [SMD]"]
  X2 = Stepper Motor - Unipolar
  Driver_PCB_Y = ULN2003A [package="SO16 [SMD]"]
  Y = Stepper Motor - Unipolar
  Driver_PCB_Z = ULN2003A [package="SO16 [SMD]"]
  Z = Stepper Motor - Unipolar

nets:
  N1: Часть1.D8, Driver_PCB_Y.In_5
  N2: Часть1.D9_PWM, Driver_PCB_Y.In_7
  N3: Часть1.D10_PWM/SS, Driver_PCB_Z.In_1
  N4: Часть1.D11_PWM/MOSI, Driver_PCB_Z.In_3
  N5: Часть1.D12/MISO, Driver_PCB_Z.In_5
  N6: Часть1.D13/SCK, Driver_PCB_Z.In_7
  N7: Часть1.D2, Driver_PCB_X1.In_1, Driver_PCB_X2.In_1
  N8: Часть1.D3_PWM, Driver_PCB_X1.In_3, Driver_PCB_X2.In_3
  N9: Часть1.D4, Driver_PCB_X1.In_5, Driver_PCB_X2.In_5
  N10: Часть1.D5_PWM, Driver_PCB_X1.In_7, Driver_PCB_X2.In_7
  N11: Часть1.D6_PWM, Driver_PCB_Y.In_1
  N12: Часть1.D7, Driver_PCB_Y.In_3
  N13: Часть1.GND, Driver_PCB_X1.0V, Driver_PCB_X2.0V, Driver_PCB_Y.0V, Driver_PCB_Z.0V
  N14: Часть1.VIN, Driver_PCB_X1.COM_-_Common, X1.COMMON_2, Driver_PCB_X2.COM_-_Common, X2.COMMON_2, Driver_PCB_Y.COM_-_Common, Y.COMMON_2, Driver_PCB_Z.COM_-_Common, Z.COMMON_2
  N15: Driver_PCB_X1.Out_7, X1.D
  N16: Driver_PCB_X1.Out_5, X1.C
  N17: Driver_PCB_X1.Out_3, X1.B
  N18: Driver_PCB_X1.Out_1, X1.A
  N19: Driver_PCB_X2.Out_7, X2.D
  N20: Driver_PCB_X2.Out_5, X2.C
  N21: Driver_PCB_X2.Out_3, X2.B
  N22: Driver_PCB_X2.Out_1, X2.A
  N23: Driver_PCB_Y.Out_7, Y.D
  N24: Driver_PCB_Y.Out_5, Y.C
  N25: Driver_PCB_Y.Out_3, Y.B
  N26: Driver_PCB_Y.Out_1, Y.A
  N27: Driver_PCB_Z.Out_7, Z.D
  N28: Driver_PCB_Z.Out_5, Z.C
  N29: Driver_PCB_Z.Out_3, Z.B
  N30: Driver_PCB_Z.Out_1, Z.A
