# Fritzing sketch id1088_Placa_0 (saved by Fritzing 0.9.3b)
circuit board: 10.4093cm x 6.05993cm
breadboards: 1

parts:
  Arduino_UNO = Arduino Uno (Rev3)
  Pololu_Eje_Y = Pololu A4988 [package=SO16]
  Pololu_Eje_X = Pololu A4988 [package=SO16]
  Componente1 = Thumb Joystick  # not connected
  Componente2 = MicroSD Card Module
  LCM1602_IIC1 = LCD convertidor I2C [part_number="LCM1602 IIC" chip_label="LCM1602 IIC"]
  LCD1 = LCD screen
  J1 = female pin header, 2 pins [form="♀ (female)"]
  S1 = Pushbutton [package="[THT]"]
  R1 = Resistor [tolerance=±5% resistance=220 package=THT]
  U1 = Voltage Regulator - 5V [package="TO220 [THT]"]
  C1 = Electrolytic Capacitor [capacitance=100nF package="100 mil [THT, electrolytic]"]
  C2 = Electrolytic Capacitor [capacitance=100nF package="100 mil [THT, electrolytic]"]
  Power_plug1 = Power plug  # not connected

nets:
  N1: Arduino_UNO.D8, Pololu_Eje_Y.RESET, Pololu_Eje_Y.SLEEP
  N2: Arduino_UNO.D9_PWM, Pololu_Eje_Y.STEP
  N3: Arduino_UNO.D10_PWM/SS, Componente2.MISO
  N4: Arduino_UNO.D11_PWM/MOSI, Componente2.MOSI
  N5: Arduino_UNO.D12/MISO, Componente2.SCK
  N6: Arduino_UNO.D13/SCK, Componente2.CS
  GND: Arduino_UNO.GND, Pololu_Eje_Y.GND, Pololu_Eje_X.GND, Componente2.GND, J1.pin2, R1.Pin_0, U1.output_voltage, C1.+
  VDD: Arduino_UNO.D2, Arduino_UNO.5V, Pololu_Eje_Y.VDD, Pololu_Eje_X.VDD, Componente2.VCC, S1.Pin_1, S1.Pin_2
  N7: Arduino_UNO.D3_PWM, J1.pin1
  N8: Arduino_UNO.D4, Pololu_Eje_X.DIR
  N9: Arduino_UNO.D5_PWM, Pololu_Eje_X.RESET, Pololu_Eje_X.SLEEP
  N10: Arduino_UNO.D6_PWM, Pololu_Eje_X.STEP
  N11: Arduino_UNO.D7, Pololu_Eje_Y.DIR
  N12: Pololu_Eje_Y.VMOT, Pololu_Eje_X.VMOT
  N13: LCM1602_IIC1.connector0, LCD1.VSS
  N14: LCM1602_IIC1.connector1, LCD1.VDD
  N15: LCM1602_IIC1.connector2, LCD1.V0
  N16: LCM1602_IIC1.connector3, LCD1.RS
  N17: LCM1602_IIC1.connector4, LCD1.R/W
  N18: LCM1602_IIC1.connector5, LCD1.E
  N19: LCM1602_IIC1.connector6, LCD1.DB0
  N20: LCM1602_IIC1.connector7, LCD1.DB1
  N21: LCM1602_IIC1.connector8, LCD1.DB2
  N22: LCM1602_IIC1.connector9, LCD1.DB3
  N23: LCM1602_IIC1.connector10, LCD1.DB4
  N24: LCM1602_IIC1.connector11, LCD1.DB5
  N25: LCM1602_IIC1.connector12, LCD1.DB6
  N26: LCM1602_IIC1.connector13, LCD1.DB7
  N27: LCM1602_IIC1.connector14, LCD1.LED+
  N28: LCM1602_IIC1.connector15, LCD1.LED-
  N29: LCM1602_IIC1.connector20, LCM1602_IIC1.connector21
  N30: S1.Pin_3, S1.Pin_4, R1.Pin_1
  N31: U1.input_voltage, C2.+
  N32: U1.GND, C1.-, C2.-

notes:
  +
  -
