# Fritzing sketch id108_3.5mm_audio_switch_0 (saved by Fritzing 0.8.7b)
circuit board: 4.64812cm x 2.95814cm
breadboards: 1

parts:
  U1 = 3.5mm Audio Jack [package=audio-jack-3.5mm-smd]
  U2 = 3.5mm Audio Jack [package=audio-jack-3.5mm-smd]
  U3 = 3.5mm Audio Jack [package=audio-jack-3.5mm-smd]
  S7 = SPST Switch [package=switche-dpdt]
  S8 = SPST Switch [package=switche-dpdt]

nets:
  N1: U1.RIGHT, S8.O
  N2: U1.LEFT, S7.S
  N3: U2.RIGHT, S8.S
  N4: U2.LEFT, S7.O
  N5: U3.RIGHT, S8.P
  N6: U3.LEFT, S7.P
