# Fritzing sketch id1090_Sterownik_pieca_0 (saved by Fritzing 0.9.2b)
circuit board: 8.46667cm x 5.64444cm

parts:
  Part1 = Arduino Pro Mini v13
  LCD1 = LCD screen
  S1 = Momentary Switch [package=ksa_sealed_tac_switch]
  S2 = Momentary Switch [package=ksa_sealed_tac_switch]
  S3 = Momentary Switch [package=ksa_sealed_tac_switch]
  LED1 = LEDs [package=led10mm]
  IC1 = Voltage Regulator [package=to-220-alt]
  C1 = Ceramic Capacitor [capacitance=100nF package="200 mil [THT, multilayer]"]
  VCC1 = Battery block 9V
  R1 = Trimmer Potentiometer [maximum_resistance=10kΩ package=THT]
  U1 = TEMPERATURE-SENSOR [package=to-92]
  R2 = Temperature Sensor (Thermistor) [thermistor_type=NTC package=THT]
  R3 = Resistor [tolerance=±5% resistance=100 package=THT]
  U2 = RELAY [package=relay-g5q]
  U3 = RELAY [package=relay-g5q]

nets:
  N1: Part1.VCC, IC1.OUT, C1.0
  GND: Part1.GND, IC1.IN, C1.1, VCC1.-, U1.GND
  N2: Part1.A3, R2.pin_1, R3.Pin_0
  N3: Part1.A0, S3.1
  N4: Part1.D13/SCK, LED1.C
  N5: Part1.D12/MISO, S2.1
  N6: Part1.D11_PWM/MOSI, S1.1
  N7: Part1.D10_PWM/SS, U1.ADJ
  N8: Part1.D9_PWM, U2.COIL2
  N9: Part1.D8, U3.COIL2
  N10: Part1.D7, LCD1.RS
  N11: Part1.D6_PWM, LCD1.E
  N12: Part1.D5_PWM, LCD1.DB4
  N13: Part1.D4, LCD1.DB5
  N14: Part1.D3_PWM, LCD1.DB6
  N15: Part1.D2, LCD1.DB7
  N16: LCD1.V0, R1.wiper
  N17: S1.4, R3.Pin_1

notes:
  DS18B20
  PT100
  100
