# Fritzing sketch id1091_Code_Oscillator_LED_0 (saved by Fritzing 0.9.3b)
breadboards: 1

parts:
  Part2 = Arduino Mega 2560 (Rev3)
  R1 = Resistor [tolerance=±5% resistance=10 package=THT]
  S1 = Round Pushbutton
  R3 = Rotary Potentiometer (Small) [maximum_resistance=100kΩ package=THT]
  SPKR1 = Loudspeaker
  LED1 = LED - 5mm [color="Red (633nm)" package="5 mm [THT]"]
  R4 = Resistor [tolerance=±5% resistance=220 package=THT]

nets:
  N1: Part2.D13_PWM, R4.Pin_1
  N2: Part2.D8_PWM, R3.wiper
  N3: Part2.5V, S1.leg0
  N4: Part2.GND, R1.Pin_1, SPKR1.pin1, LED1.cathode
  N5: Part2.D2_PWM, R1.Pin_0, S1.leg1
  N6: R3.leg1, SPKR1.pin2
  N7: LED1.anode, R4.Pin_0

notes:
  Morse Code Straight Key to be used where push button is placed
