# Fritzing sketch id1092_bikeSmart_0 (saved by Fritzing 0.9.3b)
breadboards: 2

parts:
  LCD1 = LCD screen
  R1 = Photocell (LDR) [package=THT]
  R2 = Rotary Potentiometer (Small) [maximum_resistance=100kΩ package=THT]
  R3 = Rotary Potentiometer (Small) [maximum_resistance=100kΩ package=THT]
  Part1 = Arduino Uno (Rev3)
  C1 = Capacitor Polarized [package=cpol-radial-100uf-25v]
  Part2 = Thumb Joystick
  R4 = Resistor [tolerance=±5% resistance=220 package=THT]
  R5 = Resistor [tolerance=±5% resistance=220 package=THT]
  Part4 = BME280 Breakout  # not connected

nets:
  GND: LCD1.VSS, LCD1.R/W, LCD1.LED-, R2.leg1, R3.leg1, Part1.GND, C1.-, Part2.GND, R4.Pin_0
  VDD: LCD1.VDD, R1.pin_1, R2.leg2, R3.leg2, Part1.5V, C1.+, Part2.VCC, R5.Pin_1
  N1: LCD1.V0, R3.wiper
  N2: LCD1.RS, Part1.D12/MISO
  N3: LCD1.E, Part1.D11_PWM/MOSI
  N4: LCD1.DB4, Part1.D10_PWM/SS
  N5: LCD1.DB5, Part1.D9_PWM
  N6: LCD1.DB6, Part1.D8
  N7: LCD1.DB7, Part1.D7
  N8: LCD1.LED+, R5.Pin_0
  N9: R1.pin_0, Part1.A3, R4.Pin_1
  N10: R2.wiper, Part1.A1
  N11: Part1.A0, Part2.HORZ

notes:
  I got DS1302 but there wasnt here
  , so I  just take it to present
