# Fritzing sketch id1093_Fritzingnew_0 (saved by Fritzing 0.9.2b)
breadboards: 1

parts:
  Bauteil1 = Arduino Uno (Rev3)
  S2 = Pushbutton [package="[THT]"]
  J1 = Piezo Speaker
  LED1 = LED - 5mm [color="Red (633nm)" package="5 mm [THT]"]
  R2 = Resistor [tolerance=±5% resistance=1.5k package=THT]
  LED2 = LED - 5mm [color="Red (633nm)" package="5 mm [THT]"]
  R1 = Resistor [tolerance=±5% resistance=1.5 package=THT]
  S1 = Pushbutton [package="[THT]"]

nets (from the schematic view):
  N1: Bauteil1.D8, J1.pin1
  N2: Bauteil1.GND, J1.pin2
  N3: Bauteil1.D2, S1.Pin_1, S1.Pin_2
  N4: Bauteil1.D3_PWM, S2.Pin_1, S2.Pin_2
  N5: Bauteil1.D4, R2.Pin_1
  N6: Bauteil1.D5_PWM, R1.Pin_1
  N7: S2.Pin_3, S2.Pin_4, LED2.cathode
  N8: LED1.cathode, R2.Pin_0
  N9: S1.Pin_3, S1.Pin_4

notes:
  r]
