# Fritzing sketch id1094_Coil_Gun_0 (saved by Fritzing 0.8.5b)
breadboards: 1

parts:
  L1 = Solenoid
  C1 = Tantalum Capacitor [capacitance=1μF package="100 mil [THT, tantalum]"]
  C2 = Tantalum Capacitor [capacitance=1μF package="100 mil [THT, tantalum]"]
  C3 = Tantalum Capacitor [capacitance=1μF package="100 mil [THT, tantalum]"]
  C4 = Tantalum Capacitor [capacitance=1μF package="100 mil [THT, tantalum]"]
  BAT1 = Battery Holders [package=battery-aa-kit]
  BAT2 = Battery Holders [package=battery-aa-kit]
  BAT3 = Battery Holders [package=battery-aa-kit]
  BAT4 = Battery Holders [package=battery-aa-kit]
  BAT5 = Battery Holders [package=battery-aa-kit]
  BAT6 = Battery Holders [package=battery-aa-kit]
  BAT7 = Battery Holders [package=battery-aa-kit]
  U1 = BATTERY-2 [package=battery-aaa]
  U2 = TOUCH [package=touch2]

nets:
  N1: L1.pin1, U2.T2
  N2: L1.pin2, C1.+, C2.+, C3.+, C4.+, BAT4.-
  N3: C1.-, C2.-, C3.-, C4.-
  N4: BAT1.+, BAT5.-
  N5: BAT1.-, BAT2.+
  N6: BAT2.-, BAT3.+
  N7: BAT3.-, BAT4.+
  N8: BAT5.+, BAT6.-
  N9: BAT6.+, BAT7.-
  N10: BAT7.+, U1.-1
  N11: U1.+1, U2.T1
