# Fritzing sketch id1095_Coin_Cell_Amplifier_0 (saved by Fritzing 0.9.2b)
circuit board: 2.5cm x 2.5cm
breadboards: 1

parts:
  C1 = Ceramic Capacitor [capacitance=1µF package="100 mil [THT, multilayer]"]
  J1-_Input = female pin header, 2 pins [form="♀ (female)"]
  R1 = Resistor [tolerance=±5% resistance=330k package=THT]
  R2 = Resistor [tolerance=±5% resistance=100k package=THT]
  R4 = Resistor [tolerance=±5% resistance=330 package=THT]
  R5 = Resistor [tolerance=±5% resistance=150 package=THT]
  C2 = Electrolytic Capacitor [capacitance=0.22mF voltage=20V package="100 mil [THT, electrolytic]"]
  R3 = Resistor [tolerance=±5% resistance=2.2k package=THT]
  C2_2 = Ceramic Capacitor [capacitance=10µF package="100 mil [THT, multilayer]"]
  Output = female pin header, 2 pins [form="♀ (female)"]
  J3_-_Power = female pin header, 2 pins [form="♀ (female)"]
  S1 = Toggle Switch [package=THT]
  R6 = Resistor [tolerance=±5% resistance=680 package=THT]
  LED1 = LED - 5mm [color="Red (633nm)" package="5 mm [THT]"]
  Q1 = NPN-Transistor [package="TO92 [THT]"]

nets:
  N1: C1.0, J1-_Input.pin2
  N2: C1.1, R1.Pin_1, R2.Pin_0, Q1.B
  N3: J1-_Input.pin1, R2.Pin_1, R5.Pin_1, C2.-, Output.pin2, J3_-_Power.pin1, LED1.cathode
  N4: R1.Pin_0, R3.Pin_0
  N5: R4.Pin_0, Q1.C
  N6: R4.Pin_1, R5.Pin_0, C2.+
  N7: R3.Pin_1, C2_2.0, Q1.E
  N8: C2_2.1, Output.pin1
  N9: J3_-_Power.pin2, S1.L2
  N10: S1.COM, R6.Pin_0
  N11: R6.Pin_1, LED1.anode

notes:
  Power Supply is 9Vdc
