# Fritzing sketch id1096_collidioscope_breadboard_0 (saved by Fritzing 0.9.3b)
breadboards: 1

parts:
  JP1 = Header 2 [package=molex-1x2_lock]
  JP2 = Header 2 [package=molex-1x2_lock]
  JP3 = Header 2 [package=molex-1x2_lock]
  JP4 = Header 2 [package=molex-1x2_lock]
  Teensy++1 = Teensy++ 2.0
  JP5 = Header 3 [package=molex-1x3_lock]
  JP6 = Header 3 [package=molex-1x3_lock]
  JP7 = Header 2 [package=molex-1x2_lock]
  JP8 = Header 2 [package=molex-1x2_lock]
  JP9 = Header 2 [package=molex-1x2_lock]
  JP10 = Header 2 [package=molex-1x2_lock]
  JP11 = Header 3 [package=molex-1x3_lock]
  JP12 = Header 3 [package=molex-1x3_lock]
  JP13 = Header 2 [package=molex-1x2_lock]
  JP14 = Header 2 [package=molex-1x2_lock]
  JP15 = Header 2 [package=molex-1x2_lock]
  JP16 = Header 2 [package=molex-1x2_lock]

nets:
  N1: JP1.2, Teensy++1.F1
  N2: JP2.2, Teensy++1.F0
  N3: JP3.2, Teensy++1.F3, Teensy++1.F2
  N4: JP4.2, Teensy++1.F5, Teensy++1.F4
  N5: Teensy++1.D0, JP12.2
  N6: Teensy++1.D1, JP12.3
  N7: Teensy++1.D2, JP6.2
  N8: Teensy++1.D3, JP6.3
  N9: Teensy++1.D4, JP16.2
  N10: Teensy++1.D5, JP10.2
  N11: Teensy++1.E0, JP15.2
  N12: Teensy++1.E1, JP9.2
  N13: Teensy++1.GND, Teensy++1.E6, JP5.3
  N14: Teensy++1.E7, JP5.2
  N15: Teensy++1.B0, JP13.2
  N16: Teensy++1.B1, JP14.2
  N17: Teensy++1.B3, JP7.2
  N18: Teensy++1.B4, JP8.2
  N19: Teensy++1.E4, JP11.2
  N20: Teensy++1.E5, JP11.3
