# Fritzing sketch id1098_Color_Mixing_Lamp_0 (saved by Fritzing 0.9.2b)
breadboards: 1

parts:
  Part1 = Arduino Uno (Rev3)
  LED1 = RGB LED - (4 legs) [package="5 mm [THT]"]
  R1 = Resistor [tolerance=±5% resistance=10k package=THT]
  R2 = Resistor [tolerance=±5% resistance=10k package=THT]
  R3 = Resistor [tolerance=±5% resistance=10k package=THT]
  R4 = Resistor [tolerance=±5% resistance=220 package=THT]
  R5 = Resistor [tolerance=±5% resistance=220 package=THT]
  R6 = Resistor [tolerance=±5% resistance=220 package=THT]
  R7 = PHOTOCELL [package=photocell-kit]
  R8 = PHOTOCELL [package=photocell-kit]
  R9 = PHOTOCELL [package=photocell-kit]

nets:
  N1: Part1.A0, R1.Pin_1, R8.P$1
  N2: Part1.A1, R3.Pin_1, R9.P$1
  N3: Part1.A2, R2.Pin_1, R7.P$1
  N4: Part1.D9_PWM, R6.Pin_0
  N5: Part1.D10_PWM/SS, R5.Pin_0
  N6: Part1.D11_PWM/MOSI, R4.Pin_0
  N7: Part1.5V, R7.P$2, R8.P$2, R9.P$2
  N8: Part1.GND, LED1.common_anode, R1.Pin_0, R2.Pin_0, R3.Pin_0
  N9: LED1.red_cathode, R4.Pin_1
  N10: LED1.green_cathode, R5.Pin_1
  N11: LED1.blue_cathode, R6.Pin_1
