# Fritzing sketch id1099_Sensor_0 (saved by Fritzing 0.7.12b)
breadboards: 1

parts:
  Power1 = DC Power [voltage=5]  # not connected
  R1 = Resistor [tolerance=±5% resistance=4.7k package=THT]
  R2 = Resistor [tolerance=±5% resistance=4.7k package=THT]
  ATtiny85 = attiny85 [package=dip]
  ADJD-S311 = Color Sensor Breakout ADJD-S311
  U1 = mystery part, 10 pins [chip_label=?]
  U2 = mystery part, 10 pins [chip_label=?]  # not connected

nets (from the pcb view):
  N1: R1.Pin_0, R2.Pin_0, ATtiny85.Pin_8, ADJD-S311.VCC, U1.pin10
  N2: R1.Pin_1, ATtiny85.Pin_5, ADJD-S311.SDA
  N3: R2.Pin_1, ATtiny85.Pin_7, ADJD-S311.SCL
  N4: ATtiny85.Pin_2, U1.pin8
  N5: ATtiny85.Pin_3, U1.pin9
  N6: ATtiny85.Pin_4, ADJD-S311.GND, U1.pin1
  N7: ATtiny85.Pin_6, ADJD-S311.LED

notes:
  3V3
  GND
  TX
  RX
