# Fritzing sketch id10_Photointerrupter_Common_Cathode_Emitter_0 (saved by Fritzing 0.9.2b)
breadboards: 1

parts:
  U3 = CNZ1120 [package=cnz1120]
  R3 = Resistor [tolerance=±5% resistance=300 package=THT]
  R1 = Resistor [tolerance=±5% resistance=300 package=THT]
  R2 = Resistor [tolerance=±5% resistance=10k package=THT]
  LED3 = LED - 5mm [color="Red (633nm)" package="5 mm [THT]"]

nets:
  N1: U3.1, R1.Pin_1
  GND: U3.2, U3.4, LED3.cathode
  N2: U3.3, R2.Pin_1
  5V: R3.Pin_0, R1.Pin_0, R2.Pin_0
  N3: R3.Pin_1, LED3.anode

notes:
  Подключение оптопары с общими катодом и эмиттером из печатающей техники
  +5V
  GND
