# Fritzing sketch id1100_feather_breadboard_0 (saved by Fritzing 0.9.3b)
circuit board: 5.06423cm x 2.2766cm
breadboards: 1

parts:
  Part1 = adafruit [part_number="Adafruit #2821"]
  LED1 = RGB LED (com. cathode, rgb) [package="5 mm [THT]"]
  RR = Resistor [tolerance=±5% resistance=220 package=THT]
  RG = Resistor [tolerance=±5% resistance=220 package=THT]
  RB = Resistor [tolerance=±5% resistance=220 package=THT]
  S1 = Pushbutton [package="[THT]"]

nets (from the breadboard view):
  N1: Part1.connector53, S1.Pin_1, S1.Pin_2
  N2: Part1.connector55, LED1.common_cathode
  N3: Part1.connector60, RR.Pin_0
  N4: Part1.connector61, RG.Pin_0
  N5: Part1.connector62, RB.Pin_0
  N6: Part1.connector68, S1.Pin_3, S1.Pin_4
  N7: LED1.red_anode, RR.Pin_1
  N8: LED1.green_anode, RG.Pin_1
  N9: LED1.blue_anode, RB.Pin_1
