# Fritzing sketch id1101_featherwing_proto_0 (saved by Fritzing 0.9.3b)

parts:
  FeatherWing_Proto = adafruit [part_number="Adafruit #2884"]
  RGBLED = RGB LED - (4 legs) [package="5 mm [THT]"]
  R_R = Resistor [tolerance=±5% resistance=220 package=THT]
  R_G = Resistor [tolerance=±5% resistance=220 package=THT]
  R_B = Resistor [tolerance=±5% resistance=220 package=THT]

nets (from the schematic view):
  N1: FeatherWing_Proto.connector3, R_R.Pin_0
  N2: FeatherWing_Proto.connector4, R_G.Pin_0
  N3: FeatherWing_Proto.connector5, R_B.Pin_0
  N4: FeatherWing_Proto.connector26, FeatherWing_Proto.connector164, RGBLED.common_anode
  N5: FeatherWing_Proto.connector151, FeatherWing_Proto.connector162, RGBLED.blue_cathode, R_B.Pin_1
  N6: FeatherWing_Proto.connector152, FeatherWing_Proto.connector163, RGBLED.green_cathode, R_G.Pin_1
  N7: FeatherWing_Proto.connector154, FeatherWing_Proto.connector165, RGBLED.red_cathode, R_R.Pin_1
