# Fritzing sketch id1102_Color_Mixing_Lamp_0 (saved by Fritzing 0.9.3b)
breadboards: 1

parts:
  Composant1 = Arduino Uno (Rev3)
  R1 = Resistor [tolerance=±5% resistance=10k package=THT]
  R2 = Resistor [tolerance=±5% resistance=220 package=THT]
  R3 = Resistor [tolerance=±5% resistance=10k package=THT]
  R4 = Resistor [tolerance=±5% resistance=10k package=THT]
  R5 = Resistor [tolerance=±5% resistance=220 package=THT]
  R6 = Resistor [tolerance=±5% resistance=220 package=THT]
  LED1 = RGB LED (com. cathode, rgb) [package="5 mm [THT]"]
  R7 = Photocell (LDR) [package=THT]
  R8 = Photocell (LDR) [package=THT]
  R9 = Photocell (LDR) [package=THT]

nets:
  N1: Composant1.A0, R1.Pin_1, R7.pin_0
  N2: Composant1.A1, R4.Pin_1, R8.pin_0
  N3: Composant1.A2, R3.Pin_1, R9.pin_0
  N4: Composant1.D9_PWM, R2.Pin_0
  N5: Composant1.D10_PWM/SS, R5.Pin_0
  N6: Composant1.D11_PWM/MOSI, R6.Pin_0
  N7: Composant1.5V, R7.pin_1, R8.pin_1, R9.pin_1
  N8: Composant1.GND, R1.Pin_0, R3.Pin_0, R4.Pin_0, LED1.common_cathode
  N9: R2.Pin_1, LED1.blue_anode
  N10: R5.Pin_1, LED1.green_anode
  N11: R6.Pin_1, LED1.red_anode
