# Fritzing sketch id1103_colorimetre_version_multimetre_0 (saved by Fritzing 0.7.10b)
breadboards: 1

parts:
  S2 = Pushbutton [package=THT]
  S3 = Pushbutton [package=THT]
  R1 = Rotary Potentiometer (Small) [maximum_resistance=10kΩ]
  R2 = Rotary Potentiometer (Small) [maximum_resistance=10kΩ]
  R3 = Rotary Potentiometer (Small) [maximum_resistance=10kΩ]
  LED1 = RGB LED (com. cathode, rbg) [package="5 mm [THT]"]
  R5 = Resistor [tolerance=±5% resistance=10k package=THT]
  R4 = Photocell (LDR) [package=THT]
  R6 = Resistor [tolerance=±5% resistance=2.2k package=THT]
  S1 = Pushbutton [package=THT]
  J1 = Screw terminal - 2 pins [package=THT]
  VCC1 = Battery block 9V

nets (from the breadboard view):
  N1: S2.leg0, S3.leg0, R4.pin_0, S1.leg0, VCC1.+
  N2: S2.leg1, R2.wiper
  N3: S3.leg1, R3.wiper
  N4: R1.leg1, LED1.red_anode
  N5: R1.wiper, S1.leg1
  N6: R2.leg1, LED1.blue_anode
  N7: R3.leg1, LED1.green_anode
  N8: LED1.common_cathode, R6.Pin_0
  N9: R5.Pin_0, R4.pin_1, J1.pin2
  N10: R5.Pin_1, J1.pin1
  N11: R6.Pin_1, VCC1.-

notes:
  Connecteur de raccordement du voltmètre
  Photodétecteur
  Réglage de l'intensité lumineuse
  Commande des DEL
  DEL à 3 couleurs
