# Fritzing sketch id1104_plan_montage_arduino_0 (saved by Fritzing 0.7.10b)
breadboards: 1

parts:
  Arduino1 = Arduino
  S2 = Pushbutton [package=THT]
  S3 = Pushbutton [package=THT]
  R1 = Rotary Potentiometer (Small) [maximum_resistance=10kΩ]
  R2 = Rotary Potentiometer (Small) [maximum_resistance=10kΩ]
  R3 = Rotary Potentiometer (Small) [maximum_resistance=10kΩ]
  LED1 = RGB LED (com. cathode, rbg) [package="5 mm [THT]"]
  R5 = Resistor [tolerance=±5% resistance=10k package=THT]
  R4 = Photocell (LDR) [package=THT]
  R6 = Resistor [tolerance=±5% resistance=2.2k package=THT]
  S1 = Pushbutton [package=THT]

nets (from the breadboard view):
  N1: Arduino1.GND, R5.Pin_1, R6.Pin_1
  N2: Arduino1.+5V, S2.leg0, S3.leg0, R4.pin_0, S1.leg0
  N3: Arduino1.A1, R5.Pin_0, R4.pin_1
  N4: S2.leg1, R2.wiper, R2.leg2
  N5: S3.leg1, R3.wiper
  N6: R1.leg1, LED1.red_anode
  N7: R1.wiper, S1.leg1
  N8: R2.leg1, LED1.blue_anode
  N9: R3.leg1, LED1.green_anode
