# Fritzing sketch id1105_plan_montage_multimetre_0 (saved by Fritzing 0.7.10b)
breadboards: 1

parts:
  S2 = Pushbutton [package=THT]
  S3 = Pushbutton [package=THT]
  R1 = Rotary Potentiometer (Small) [maximum_resistance=10kΩ]
  R2 = Rotary Potentiometer (Small) [maximum_resistance=10kΩ]
  R3 = Rotary Potentiometer (Small) [maximum_resistance=10kΩ]
  LED1 = RGB LED (com. cathode, rbg) [package="5 mm [THT]"]
  R5 = Resistor [tolerance=±5% resistance=10k package=THT]
  R4 = Photocell (LDR) [package=THT]
  R6 = Resistor [tolerance=±5% resistance=2.2k package=THT]
  S1 = Pushbutton [package=THT]
  J1 = Screw terminal - 2 pins [package=THT]
  VCC1 = Battery block 9V
  U1 = Voltage Regulator - 5V [package="TO220 [THT]"]

nets (from the schematic view):
  N1: S2.leg0, S3.leg0, R4.pin_0, S1.leg0, U1.output_voltage
  N2: S2.leg1, R2.leg2
  N3: S3.leg1, R3.leg2
  N4: R1.leg1, LED1.green_anode
  N5: R1.leg2, S1.leg1
  N6: R2.leg1, LED1.blue_anode
  N7: R3.leg1, LED1.red_anode
  N8: LED1.common_cathode, R6.Pin_0
  N9: R5.Pin_0, J1.pin2
  N10: R5.Pin_1, R6.Pin_1, J1.pin1, VCC1.-, U1.GND
  N11: VCC1.+, U1.input_voltage

notes:
  Connecteur de raccordement du voltmètre
  Photodétecteur
  Réglage de l'intensité lumineuse
  Commande des DEL
  DEL à 3 couleurs
