# Fritzing sketch id1106_ponte_elevatoria_pantografica_0 (saved by Fritzing 0.9.2b)
breadboards: 1

parts:
  Componente1 = Arduino Uno (Rev3)
  S1 = Pushbutton [package="[THT]"]
  S2 = Pushbutton [package="[THT]"]
  S3 = Pushbutton [package="[THT]"]
  S4 = Pushbutton [package="[THT]"]
  R3 = Resistor [tolerance=±5% resistance=220 package=THT]
  R4 = Resistor [tolerance=±5% resistance=220 package=THT]
  S5 = Pushbutton [package="[THT]"]
  S6 = Pushbutton [package="[THT]"]
  R5 = Rotary Potentiometer (Small) [maximum_resistance=100kΩ package=THT]
  R6 = Resistor [tolerance=±5% resistance=220 package=THT]
  R7 = Resistor [tolerance=±5% resistance=220 package=THT]
  R8 = Resistor [tolerance=±5% resistance=220 package=THT]
  R9 = Resistor [tolerance=±5% resistance=220 package=THT]
  R10 = Resistor [tolerance=±5% resistance=220 package=THT]
  LED2 = LED - 5mm [color="Red (633nm)" package="5 mm [THT]"]
  LED3 = LED - 5mm [color="Red (633nm)" package="5 mm [THT]"]
  LED4 = LED - 5mm [color="Red (633nm)" package="5 mm [THT]"]
  LED5 = LED - 5mm [color="Red (633nm)" package="5 mm [THT]"]
  R11 = Resistor [tolerance=±5% resistance=220 package=THT]
  R12 = Resistor [tolerance=±5% resistance=220 package=THT]
  R13 = Resistor [tolerance=±5% resistance=220 package=THT]
  R14 = Resistor [tolerance=±5% resistance=220 package=THT]
  LED6 = LED - 5mm [color="Red (633nm)" package="5 mm [THT]"]
  R15 = Resistor [tolerance=±5% resistance=220 package=THT]
  LED7 = LED - 5mm [color="Red (633nm)" package="5 mm [THT]"]

nets:
  N1: Componente1.A0, R5.wiper
  N2: Componente1.D8, LED7.anode
  N3: Componente1.D9_PWM, LED3.anode
  N4: Componente1.D10_PWM/SS, LED2.anode
  N5: Componente1.D11_PWM/MOSI, LED4.anode
  N6: Componente1.D12/MISO, LED5.anode
  N7: Componente1.D13/SCK, LED6.anode
  N8: Componente1.D2, S1.Pin_1, S1.Pin_2, R3.Pin_1
  N9: Componente1.D3_PWM, S2.Pin_1, S2.Pin_2, R4.Pin_1
  N10: Componente1.D4, S3.Pin_1, S3.Pin_2, R6.Pin_1
  N11: Componente1.D5_PWM, S4.Pin_1, S4.Pin_2, R7.Pin_1
  N12: Componente1.D6_PWM, S5.Pin_1, S5.Pin_2, R8.Pin_1
  N13: Componente1.D7, S6.Pin_1, S6.Pin_2, R9.Pin_1
  N14: Componente1.5V, R3.Pin_0, R4.Pin_0, R5.leg1, R6.Pin_0, R7.Pin_0, R8.Pin_0, R9.Pin_0, R10.Pin_0, R11.Pin_0, R12.Pin_0, R13.Pin_0, R14.Pin_0, R15.Pin_0
  N15: Componente1.GND, S1.Pin_3, S1.Pin_4, S2.Pin_3, S2.Pin_4, S3.Pin_3, S3.Pin_4, S4.Pin_3, S4.Pin_4, S5.Pin_3, S5.Pin_4, S6.Pin_3, S6.Pin_4, R5.leg2
  N16: R10.Pin_1, LED7.cathode
  N17: LED2.cathode, R12.Pin_1
  N18: LED3.cathode, R11.Pin_1
  N19: LED4.cathode, R13.Pin_1
  N20: LED5.cathode, R14.Pin_1
  N21: LED6.cathode, R15.Pin_1
