# Fritzing sketch id1107_Untitled_Sketch_2_0 (saved by Fritzing 0.9.3b)

parts:
  Componente1 = Arduino Nano (Rev3.0)
  S1 = Pushbutton [package="[THT]"]
  S2 = Pushbutton [package="[THT]"]
  K1 = Relay [part_number=FRS1B-S package=THT]
  K2 = Relay [part_number=FRS1B-S package=THT]
  R1 = Resistor [tolerance=±5% resistance=220 package=THT]
  R2 = Resistor [tolerance=±5% resistance=220 package=THT]
  M1 = Stepper Motor - Bipolar

nets:
  N1: Componente1.GND, K1.COIL1, K2.COIL1, R1.Pin_1, R2.Pin_1
  N2: Componente1.D2, K2.COIL2
  N3: Componente1.D3, K1.COIL2
  N4: Componente1.D4, S2.Pin_3, S2.Pin_4, R1.Pin_0
  N5: Componente1.D5, S1.Pin_3, S1.Pin_4, R2.Pin_0
  N6: Componente1.5V, S1.Pin_1, S1.Pin_2, S2.Pin_1, S2.Pin_2
  N7: K1.A, K2.A
  N8: K1.C1, K1.C2, M1.C
  N9: K2.C1, K2.C2, M1.D
