# Fritzing sketch id1108_led_a_ritmo_di_musica_0 (saved by Fritzing 0.8.7b)
breadboards: 1

parts:
  Componente1 = Arduino Uno (Rev3)
  LED1 = LED - 3mm [color="Blue (505nm)" package="3 mm [THT]"]
  LED2 = LED - 3mm [color="Red (633nm)" package="3 mm [THT]"]
  LED3 = LED - 3mm [color="Red (633nm)" package="3 mm [THT]"]
  LED4 = LED - 3mm [color="Yellow (595nm)" package="3 mm [THT]"]
  LED5 = LED - 3mm [color="Yellow (595nm)" package="3 mm [THT]"]
  LED6 = LED - 3mm [color="Yellow (595nm)" package="3 mm [THT]"]
  LED7 = LED - 3mm [color="Yellow (595nm)" package="3 mm [THT]"]
  LED8 = LED - 3mm [color="Yellow (595nm)" package="3 mm [THT]"]
  LED9 = LED - 3mm [color="Blue (505nm)" package="3 mm [THT]"]
  LED10 = LED - 3mm [color="Blue (505nm)" package="3 mm [THT]"]
  LED11 = LED - 3mm [color="Blue (505nm)" package="3 mm [THT]"]
  LED12 = LED - 3mm [color="Blue (505nm)" package="3 mm [THT]"]
  MIC1 = Microphone
  U1 = POT [package=trim_pot]

nets:
  N1: Componente1.A1, U1.E
  N2: Componente1.D8, LED8.anode
  N3: Componente1.D9_PWM, LED1.anode
  N4: Componente1.D10_PWM/SS, LED9.anode
  N5: Componente1.D11_PWM/MOSI, LED11.anode
  N6: Componente1.D12/MISO, LED10.anode
  N7: Componente1.D13/SCK, LED12.anode
  N8: Componente1.GND, LED1.cathode, LED2.cathode, LED3.cathode, LED4.cathode, LED5.cathode, LED6.cathode, LED7.cathode, LED8.cathode, LED9.cathode, LED10.cathode, LED11.cathode, LED12.cathode, MIC1.pin1, U1.A
  N9: Componente1.D2, LED2.anode
  N10: Componente1.D3_PWM, LED3.anode
  N11: Componente1.D4, LED4.anode
  N12: Componente1.D5_PWM, LED5.anode
  N13: Componente1.D6_PWM, LED6.anode
  N14: Componente1.D7, LED7.anode
  N15: MIC1.pin2, U1.S
