# Fritzing sketch id110_3x3x3_Cube_wiring_20131019_0 (saved by Fritzing 0.8.3b)
circuit board: 5.23183cm x 5.30793cm
breadboards: 1

parts:
  U1 = 74HC595 [package="DIP16 [THT]"]
  U2 = 74HC595 [package="DIP16 [THT]"]
  Q1 = NPN-Transistor [package="TO92 [THT]"]
  Q2 = NPN-Transistor [package="TO92 [THT]"]
  Q3 = NPN-Transistor [package="TO92 [THT]"]
  R2 = Resistor [tolerance=±5% resistance=220 package=THT]
  R3 = Resistor [tolerance=±5% resistance=220 package=THT]
  R4 = Resistor [tolerance=±5% resistance=220 package=THT]
  R5 = Resistor [tolerance=±5% resistance=220 package=THT]
  R6 = Resistor [tolerance=±5% resistance=220 package=THT]
  R7 = Resistor [tolerance=±5% resistance=220 package=THT]
  R8 = Resistor [tolerance=±5% resistance=220 package=THT]
  R9 = Resistor [tolerance=±5% resistance=220 package=THT]
  R10 = Resistor [tolerance=±5% resistance=220 package=THT]
  Layer_c = female pin header, 1 pin [form="♀ (female)"]
  Layer_b = female pin header, 1 pin [form="♀ (female)"]
  Layer_a = female pin header, 1 pin [form="♀ (female)"]
  Column_1 = female pin header, 1 pin [form="♀ (female)"]
  Column_2 = female pin header, 1 pin [form="♀ (female)"]
  Column_3 = female pin header, 1 pin [form="♀ (female)"]
  Column_4 = female pin header, 1 pin [form="♀ (female)"]
  Column_5 = female pin header, 1 pin [form="♀ (female)"]
  Column_6 = female pin header, 1 pin [form="♀ (female)"]
  Column_7 = female pin header, 1 pin [form="♀ (female)"]
  Column_8 = female pin header, 1 pin [form="♀ (female)"]
  Column_9 = female pin header, 1 pin [form="♀ (female)"]
  Arduino1 = Arduino

nets:
  N1: U1.Q1, R2.Pin_0
  N2: U1.Q2, R3.Pin_0
  N3: U1.Q3, R4.Pin_0
  N4: U1.Q4, R5.Pin_0
  N5: U1.Q5, R6.Pin_0
  N6: U1.Q6, R7.Pin_0
  N7: U1.Q7, R8.Pin_0
  GND: U1.GND, U1.OE, U2.GND, U2.OE, Q1.E, Q2.E, Q3.E, Arduino1.GND
  N8: U1.Q7', U2.DS
  VCC: U1.MR, U1.VCC, U2.MR, U2.VCC, Arduino1.+5V
  N9: U1.SH_CP, U2.SH_CP, Arduino1.D12
  N10: U1.ST_CP, U2.ST_CP, Arduino1.D8
  N11: U1.DS, Arduino1.D11
  N12: U1.Q0, R10.Pin_0
  N13: U2.Q1, Q3.B
  N14: U2.Q2, Q2.B
  N15: U2.Q3, Q1.B
  N16: U2.Q0, R9.Pin_0
  N17: Q1.C, Layer_a.pin1
  N18: Q2.C, Layer_b.pin1
  N19: Q3.C, Layer_c.pin1
  N20: R2.Pin_1, Column_2.pin1
  N21: R3.Pin_1, Column_3.pin1
  N22: R4.Pin_1, Column_4.pin1
  N23: R5.Pin_1, Column_5.pin1
  N24: R6.Pin_1, Column_6.pin1
  N25: R7.Pin_1, Column_7.pin1
  N26: R8.Pin_1, Column_8.pin1
  N27: R9.Pin_1, Column_9.pin1
  N28: R10.Pin_1, Column_1.pin1
