# Fritzing sketch id1110_555_PWM_0 (saved by Fritzing 0.9.1b)
breadboards: 1

parts:
  IC1 = General purpose bipolar Timer [package=dil-08]
  M1 = DC Motor
  J1 = Piezo Speaker
  LED1 = LED - 3mm [color="Red (633nm)" package="3 mm [THT]"]
  BAT1 = BC9VPC [package=bc9vpc]
  D1 = Zener Diode [part_number=1N4732A breakdown_voltage=12.1V package="Melf DO-213 AB [SMD]"]
  U1 = POT [package=pot_alpha_rv16af-20]
  R1 = Resistor [package="0402 [SMD]"]
  R2 = Resistor [package="0402 [SMD]"]
  C2 = Electrolytic Capacitor [capacitance=1000μF package="1010 [SMD, electrolytic]"]

nets:
  N1: IC1.GND, M1.pin_2, J1.pin2, LED1.cathode, BAT1.V-, C2.-
  N2: IC1.TRI, IC1.TRE, D1.cathode, R2.Pin_0, C2.+
  N3: IC1.OUT, M1.pin_1, J1.pin1, LED1.anode
  N4: IC1._RES, IC1.CON, IC1.VCC+, BAT1.V+, R1.Pin_1
  N5: IC1.DIS, D1.anode, U1.S
  N6: U1.A, R2.Pin_1
  N7: U1.E, R1.Pin_0

notes:
  Project: PWM
  Organization: BrainDelta
  Author: Abhi Kalyan
  Resistance and capacitance control PWM cycle, change as per applicaiton. Diode any applicable.
  use any output as required.
