# Fritzing sketch id1111_Sensor_PIR_0 (saved by Fritzing 0.7.12b)
breadboards: 1

parts:
  LED1 = LED - 5mm [color="Red (633nm)" package="5 mm [THT]"]
  J1 = Piezo Speaker
  Arduino1 = Arduino
  R1 = Resistor [tolerance=±5% resistance=220 package=THT]
  R2 = Resistor [tolerance=±5% resistance=220 package=THT]
  U1 = Adafruit PIR [part_number=189]

nets:
  N1: LED1.cathode, J1.pin1, Arduino1.GND, U1.connector0
  N2: LED1.anode, R1.Pin_0
  N3: J1.pin2, R2.Pin_0
  N4: Arduino1.D9, R1.Pin_1
  N5: Arduino1.D8, U1.connector1
  N6: Arduino1.D7, R2.Pin_1
  N7: Arduino1.+5V, U1.connector2

notes:
  Sensor PIR
