# Fritzing sketch id1112_proj_0 (saved by Fritzing 0.7.10b)
breadboards: 1

parts:
  LED1 = LED - 5mm [color="Blue (430nm)" package="5 mm [THT]"]
  R1 = Resistor [tolerance=±5% resistance=100 package=THT]
  Arduino1 = Arduino

nets:
  N1: LED1.cathode, Arduino1.GND
  N2: R1.Pin_1, Arduino1.D10
