# Fritzing sketch id1113_FanController.01_0 (saved by Fritzing 0.9.2b)
circuit board: 7.92998cm x 2.96942cm
breadboards: 1

parts:
  Part1 = Arduino Nano (Rev3.0)
  JP2 = Header 3 [package=molex-1x3_lock]
  C1 = Electrolytic Capacitor [capacitance=100µF voltage=16V package="200 mil [THT, electrolytic]"]
  T1 = LM35 Temperature Sensor [package="TO92 [THT]"]
  ULN1 = Darlington Driver [part_number=ULN2003 package=dil18]
  JP3 = Header 3 [package=molex-1x3_lock]
  C2 = Electrolytic Capacitor [capacitance=100µF voltage=16V package="200 mil [THT, electrolytic]"]
  JP1 = Header 3 [package=molex-1x3_lock]

nets:
  GND: Part1.GND, T1.GND, ULN1.9, JP1.1
  N1: Part1.D3, ULN1.1
  N2: Part1.D5, ULN1.3
  12V: Part1.VIN, JP2.2, C1.+, ULN1.10, JP3.2, C2.+, JP1.2
  N3: Part1.5V, T1.+Vs
  N4: Part1.A1, T1.Vout
  N5: JP2.1, C1.-, ULN1.18
  N6: ULN1.16, JP3.1, C2.-
