# Fritzing sketch id1114_FanController.ProMini_0 (saved by Fritzing 0.9.2b)
circuit board: 8.513cm x 2.896cm
breadboards: 1

parts:
  Part1 = Arduino Pro Mini v13
  T2 = LM35 Temperature Sensor [package="TO92 [THT]"]
  ULN2 = Darlington Driver [part_number=ULN2003 package=dil18]
  JP2 = Header 3 [package=molex-1x3_lock]
  C1 = Electrolytic Capacitor [capacitance=100µF voltage=16V package="200 mil [THT, electrolytic]"]
  JP3 = Header 3 [package=molex-1x3_lock]
  C2 = Electrolytic Capacitor [capacitance=100µF voltage=16V package="200 mil [THT, electrolytic]"]
  J1 = COMPUTER-PERIPHERAL-POWER [package=computer-peripheral-power-ra]

nets:
  5V: Part1.RAW, T2.+Vs, J1.5V
  GND: Part1.GND, T2.GND, ULN2.9, J1.GND, J1.NC
  N1: Part1.A1, T2.Vout
  N2: Part1.D5_PWM, ULN2.3
  N3: Part1.D3_PWM, ULN2.1
  12V: ULN2.10, JP2.2, C1.+, JP3.2, C2.+, J1.12V
  N4: ULN2.16, JP3.1, C2.-
  N5: ULN2.18, JP2.1, C1.-
