# Fritzing sketch id1116_Carrega_de_condensador (saved by Fritzing 0.4.3b)
breadboards: 1

parts:
  VCC1 = obsolete Battery
  LED1 = Red LED - 5mm
  S1 = Toggle Switch [package=THT]
  C1 = Electrolytic Capacitor [package=THT]
  R1 = Resistor [resistance=1M package=THT]

nets:
  N1: VCC1.-, LED1.cathode, C1.-
  N2: VCC1.+, S1.L1
  N3: LED1.anode, S1.L2
  N4: S1.COM, R1.Pin_1
  N5: C1.+, R1.Pin_0
