# Fritzing sketch id1117_SyncStripper_0 (saved by Fritzing 0.8.7b)
circuit board: 2.3549cm x 1.81296cm
breadboards: 1

parts:
  LM1881N = IC, DIP package, 8 pins [chip_label=IC]
  in = Pad [width=5 height=2.35353797132617 connect=center]
  GND = Pad [width=5 height=2.35353797132617 connect=center]
  out = Pad [width=5 height=2.35353797132617 connect=center]
  Vcc = Pad [width=5 height=2.35353797132617 connect=center]
  C1 = Ceramic Capacitor [capacitance=100nF package="100 mil [THT, multilayer]"]
  C2 = Ceramic Capacitor [capacitance=100nF package="100 mil [THT, multilayer]"]
  R1 = Resistor [tolerance=±5% resistance=220 package=THT]

nets:
  N1: LM1881N.pin1, out.pad
  N2: LM1881N.pin2, C1.1
  N3: LM1881N.pin4, GND.pad, C2.1, R1.Pin_1
  N4: LM1881N.pin6, C2.0, R1.Pin_0
  N5: LM1881N.pin8, Vcc.pad
  N6: in.pad, C1.0
