# Fritzing sketch id1118_CompBatt_0 (saved by Fritzing 0.9.0b)
circuit board: 4.29762cm x 5.24133cm
breadboards: 1

parts:
  R1 = Trimmer Potentiometer [maximum_resistance=10kΩ package=THT]
  VCC = Battery
  R2 = Resistor [tolerance=±5% resistance=33k package=THT]
  DZ = Zener Diode [part_number=1N4733A breakdown_voltage=5.1V package="300 mil [THT]"]
  Q1 = NPN-Transistor [part_number=2N3904 package="TO92 [THT]"]
  LED1 = LED - 5mm [color="Green (555nm)" package="5 mm [THT]"]
  R3 = Resistor [tolerance=±5% resistance=470 package=THT]
  LED2 = LED - 5mm [color="Red (633nm)" package="5 mm [THT]"]
  R4 = Resistor [tolerance=±5% resistance=470 package=THT]
  Q2 = NPN-Transistor [package="TO92 [THT]"]

nets:
  N1: R1.leg1, VCC.-, Q1.E, Q2.E
  N2: R1.wiper, R2.Pin_0
  N3: R1.leg2, VCC.+, LED1.anode, LED2.anode
  N4: R2.Pin_1, DZ.cathode
  N5: DZ.anode, Q1.B
  N6: Q1.C, R3.Pin_1, Q2.B
  N7: LED1.cathode, R3.Pin_0
  N8: LED2.cathode, R4.Pin_0
  N9: R4.Pin_1, Q2.C

notes:
  COMPROBADOR CARGA BATERIAS, Comprobador de carga de baterias. Apto para diferentes voltajes., 0
  PCB - 000 - Rev.0
  RFS 2016
  Vin. Dz R3/R4
  6v. <=3,3v. 390 Ohm
  9v. <=5,1v. 470 Ohm
  12v. Entre 6v. y 8v. 1KOhm
  24v. +- 18v. 1,5KOhm
  Observaciones:
  - Para ajustar encendido de leds, conectar fuente variable a la entrada y ajustar preset de 10KOhm (R1)
  COMPROBADOR DE CARGA DE BATERIAS
