# Fritzing sketch id1119_UltrasonicoLimite20cm1led_0 (saved by Fritzing 0.9.3b)
breadboards: 1

parts:
  Componente2 = Arduino Uno (Rev3)
  U2 = generic_sip_4_300mil.fzp [chip_label=IC]

nets:
  N1: Componente2.GND, U2.connector3
  N2: Componente2.D2, U2.connector2
  N3: Componente2.D3_PWM, U2.connector1
  N4: Componente2.3V3, U2.connector0
