# Fritzing sketch id111_LED_Cube_3x3x3_0 (saved by Fritzing 0.9.1b)
circuit board: 16.9333cm x 5.64444cm
breadboards: 10

parts:
  LED1 = LED - 5mm [color="Red (633nm)" package="5 mm [THT]"]
  LED2 = LED - 5mm [color="Red (633nm)" package="5 mm [THT]"]
  LED3 = LED - 5mm [color="Red (633nm)" package="5 mm [THT]"]
  LED4 = LED - 5mm [color="Red (633nm)" package="5 mm [THT]"]
  LED5 = LED - 5mm [color="Red (633nm)" package="5 mm [THT]"]
  LED6 = LED - 5mm [color="Red (633nm)" package="5 mm [THT]"]
  LED7 = LED - 5mm [color="Red (633nm)" package="5 mm [THT]"]
  LED8 = LED - 5mm [color="Red (633nm)" package="5 mm [THT]"]
  LED9 = LED - 5mm [color="Red (633nm)" package="5 mm [THT]"]
  R1 = Resistor [tolerance=±5% resistance=220 package=THT]
  R2 = Resistor [tolerance=±5% resistance=220 package=THT]
  R3 = Resistor [tolerance=±5% resistance=220 package=THT]
  R4 = Resistor [tolerance=±5% resistance=220 package=THT]
  R5 = Resistor [tolerance=±5% resistance=220 package=THT]
  R6 = Resistor [tolerance=±5% resistance=220 package=THT]
  R7 = Resistor [tolerance=±5% resistance=220 package=THT]
  R8 = Resistor [tolerance=±5% resistance=220 package=THT]
  R9 = Resistor [tolerance=±5% resistance=220 package=THT]
  LED10 = LED - 5mm [color="Red (633nm)" package="5 mm [THT]"]
  LED11 = LED - 5mm [color="Red (633nm)" package="5 mm [THT]"]
  LED12 = LED - 5mm [color="Red (633nm)" package="5 mm [THT]"]
  LED13 = LED - 5mm [color="Red (633nm)" package="5 mm [THT]"]
  LED14 = LED - 5mm [color="Red (633nm)" package="5 mm [THT]"]
  LED15 = LED - 5mm [color="Red (633nm)" package="5 mm [THT]"]
  LED16 = LED - 5mm [color="Red (633nm)" package="5 mm [THT]"]
  LED17 = LED - 5mm [color="Red (633nm)" package="5 mm [THT]"]
  LED18 = LED - 5mm [color="Red (633nm)" package="5 mm [THT]"]
  R10 = Resistor [tolerance=±5% resistance=220 package=THT]
  R11 = Resistor [tolerance=±5% resistance=220 package=THT]
  R12 = Resistor [tolerance=±5% resistance=220 package=THT]
  R13 = Resistor [tolerance=±5% resistance=220 package=THT]
  R14 = Resistor [tolerance=±5% resistance=220 package=THT]
  R15 = Resistor [tolerance=±5% resistance=220 package=THT]
  R16 = Resistor [tolerance=±5% resistance=220 package=THT]
  R17 = Resistor [tolerance=±5% resistance=220 package=THT]
  R18 = Resistor [tolerance=±5% resistance=220 package=THT]
  LED19 = LED - 5mm [color="Red (633nm)" package="5 mm [THT]"]
  LED20 = LED - 5mm [color="Red (633nm)" package="5 mm [THT]"]
  LED21 = LED - 5mm [color="Red (633nm)" package="5 mm [THT]"]
  LED22 = LED - 5mm [color="Red (633nm)" package="5 mm [THT]"]
  LED23 = LED - 5mm [color="Red (633nm)" package="5 mm [THT]"]
  LED24 = LED - 5mm [color="Red (633nm)" package="5 mm [THT]"]
  LED25 = LED - 5mm [color="Red (633nm)" package="5 mm [THT]"]
  LED26 = LED - 5mm [color="Red (633nm)" package="5 mm [THT]"]
  LED27 = LED - 5mm [color="Red (633nm)" package="5 mm [THT]"]
  R19 = Resistor [tolerance=±5% resistance=220 package=THT]
  R20 = Resistor [tolerance=±5% resistance=220 package=THT]
  R21 = Resistor [tolerance=±5% resistance=220 package=THT]
  R22 = Resistor [tolerance=±5% resistance=220 package=THT]
  R23 = Resistor [tolerance=±5% resistance=220 package=THT]
  R24 = Resistor [tolerance=±5% resistance=220 package=THT]
  R25 = Resistor [tolerance=±5% resistance=220 package=THT]
  R26 = Resistor [tolerance=±5% resistance=220 package=THT]
  R27 = Resistor [tolerance=±5% resistance=220 package=THT]
  U1 = 74HC595 [package="DIP16 [THT]"]
  U2 = 74HC595 [package="DIP16 [THT]"]
  Q1 = NPN-Transistor [package="TO92 [THT]"]
  Q2 = NPN-Transistor [package="TO92 [THT]"]
  Q3 = NPN-Transistor [package="TO92 [THT]"]
  part = Arduino Uno (Rev3)  # not connected
  Bauteil1 = Arduino Uno (Rev3)

nets:
  N1: LED1.cathode, LED2.cathode, LED3.cathode, LED4.cathode, LED5.cathode, LED6.cathode, LED7.cathode, LED8.cathode, LED9.cathode, Q1.C
  N2: LED1.anode, R8.Pin_0
  N3: LED2.anode, R5.Pin_0
  N4: LED3.anode, R2.Pin_0
  N5: LED4.anode, R9.Pin_0
  N6: LED5.anode, R1.Pin_0
  N7: LED6.anode, R4.Pin_0
  N8: LED7.anode, R7.Pin_0
  N9: LED8.anode, R3.Pin_0
  N10: LED9.anode, R6.Pin_0
  N11: R1.Pin_1, R18.Pin_1, R21.Pin_1, U1.Q0
  N12: R2.Pin_1, R12.Pin_1, R22.Pin_1
  N13: R3.Pin_1, R16.Pin_1, R27.Pin_1, U1.Q7
  N14: R4.Pin_1, R14.Pin_1, U1.Q6
  N15: R5.Pin_1, R15.Pin_1, R23.Pin_1, U1.Q5
  N16: R6.Pin_1, R11.Pin_1, R20.Pin_1, U1.Q4
  N17: R7.Pin_1, R10.Pin_1, R19.Pin_1, U1.Q3
  N18: R8.Pin_1, R13.Pin_1, R24.Pin_1, R26.Pin_1, U1.Q2
  N19: R9.Pin_1, R17.Pin_1, R25.Pin_1, U1.Q1
  N20: LED10.cathode, LED11.cathode, LED12.cathode, LED13.cathode, LED14.cathode, LED15.cathode, LED16.cathode, LED17.cathode, LED18.cathode, Q3.C
  N21: LED10.anode, R11.Pin_0
  N22: LED11.anode, R14.Pin_0
  N23: LED12.anode, R10.Pin_0
  N24: LED13.anode, R16.Pin_0
  N25: LED14.anode, R13.Pin_0
  N26: LED15.anode, R18.Pin_0
  N27: LED16.anode, R17.Pin_0
  N28: LED17.anode, R15.Pin_0
  N29: LED18.anode, R12.Pin_0
  N30: LED19.cathode, LED20.cathode, LED21.cathode, LED22.cathode, LED23.cathode, LED24.cathode, LED25.cathode, LED26.cathode, LED27.cathode, Q2.C
  N31: LED19.anode, R23.Pin_0
  N32: LED20.anode, R25.Pin_0
  N33: LED21.anode, R26.Pin_0
  N34: LED22.anode, R21.Pin_0
  N35: LED23.anode, R27.Pin_0
  N36: LED24.anode, R19.Pin_0
  N37: LED25.anode, R24.Pin_0
  N38: LED26.anode, R20.Pin_0
  N39: LED27.anode, R22.Pin_0
  GND: U1.GND, U1.OE, U2.GND, U2.OE, Q1.E, Q2.E, Q3.E, Bauteil1.GND
  N40: U1.Q7', U2.DS
  N41: U1.MR, U1.VCC
  N42: U1.SH_CP, Bauteil1.D12/MISO
  N43: U1.ST_CP, U2.ST_CP, Bauteil1.D8
  N44: U1.DS, Bauteil1.D11_PWM/MOSI
  N45: U2.Q1, Q1.B
  N46: U2.Q2, Q3.B
  N47: U2.Q3, Q2.B
  VCC: U2.MR, U2.VCC, Bauteil1.5V
