# Fritzing sketch id1120_allparts_0 (saved by Fritzing 0.9.2b)
breadboards: 1

parts:
  part = Arduino Uno (Rev3)
  part_2 = POT [package=pot_mammoth]
  part_3 = Loudspeaker
  R2 = Resistor [tolerance=±5% resistance=220 package=THT]
  R1 = Photocell (LDR) [part_number="100k LDR" package=THT]

nets:
  N1: part.A0, R2.Pin_0, R1.pin_1
  N2: part.A1, part_2.A
  N3: part.D13/SCK, part_3.pin2
  GND: part.GND, part_2.S, part_3.pin1, R1.pin_0
  N4: part.VIN, part_2.E, R2.Pin_1
