# Fritzing sketch id1122_Conectando_LCD_a_arduino_0 (saved by Fritzing 0.9.2b)
breadboards: 1

parts:
  LCD1 = LCD screen
  Parte1 = Arduino Uno (Rev3)
  R1 = Rotary Potentiometer (Large) [maximum_resistance=100kΩ package=THT]

nets:
  N1: LCD1.VSS, R1.wiper
  N2: LCD1.VDD, Parte1.D7
  N3: LCD1.V0, LCD1.LED-, Parte1.GND, R1.leg1
  N4: LCD1.RS, Parte1.D8
  N5: LCD1.DB4, Parte1.D9_PWM
  N6: LCD1.DB5, Parte1.D10_PWM/SS
  N7: LCD1.DB6, Parte1.D11_PWM/MOSI
  N8: LCD1.DB7, Parte1.D12/MISO
  N9: LCD1.LED+, Parte1.5V, R1.leg2
