# Fritzing sketch id1123_base_arduino_hc_06_0 (saved by Fritzing 0.9.3b)
breadboards: 1

parts:
  Componente1 = Arduino Uno (Rev3)
  BT1 = Bluetooth HC-06u

nets:
  N1: Componente1.D0/RX, BT1.connector2
  N2: Componente1.D1/TX, BT1.connector3
  N3: Componente1.GND, BT1.connector1
  N4: Componente1.VIN, BT1.connector0
