# Fritzing sketch id1124_LM35_0 (saved by Fritzing 0.9.3b)
breadboards: 1

parts:
  T1 = LM35 Temperature Sensor [package="TO92 [THT]"]
  BAT1 = BC9VPC [package=bc9vpc]

nets:
  N1: T1.+Vs, BAT1.V+
  N2: T1.GND, BAT1.V-
