# Fritzing sketch id1125_conexciones_Robot__SamyHuerta_0 (saved by Fritzing 0.9.3b)
breadboards: 1

parts:
  LED1 = LED - 5mm [color="Red (633nm)" package="5 mm [THT]"]
  M1 = DC Motor
  TCRT1 = TCRT5000_sensor_module.fzp [part_number=151608]
  ultasonoco = IC, SIP package, 4 pins [chip_label=IC]
  BT-06 = Bluetooth HC-05 Macho
  Componente2 = Arduino Uno (Rev3)
  U2 = LIPO-1000mAh [package=lipo-1000]
  L298N = Ponte-H L298N
  U3 = IC, SIP package, 4 pins [chip_label=IC]
  TCRT2 = TCRT5000_sensor_module.fzp [part_number=151608]
  LED = LED - 5mm [color="Red (633nm)" package="5 mm [THT]"]
  R3 = PHOTOCELL [package=photocell-kit]
  M2 = DC Motor
  R7 = Resistor [tolerance=±5% resistance=10k package=THT]
  R10 = Resistor [tolerance=±5% resistance=10k package=THT]
  R11 = Resistor [tolerance=±5% resistance=10k package=THT]
  R13 = Resistor [tolerance=±5% resistance=220 package=THT]
  R14 = Resistor [tolerance=±5% resistance=220 package=THT]
  R16 = Resistor [tolerance=±5% resistance=10k package=THT]
  TCRT3 = TCRT5000_sensor_module.fzp [part_number=151608]
  TCRT4 = TCRT5000_sensor_module.fzp [part_number=151608]
  R17 = Resistor [tolerance=±5% resistance=220 package=THT]
  R18 = Resistor [tolerance=±5% resistance=220 package=THT]
  R19 = Resistor [tolerance=±5% resistance=10k package=THT]
  R20 = Resistor [tolerance=±5% resistance=10k package=THT]
  R2 = PHOTOCELL [package=photocell-kit]

nets:
  GND: LED1.cathode, TCRT1.connector1, TCRT1.connector3, ultasonoco.pin4, BT-06.GND, Componente2.GND, U3.pin4, LED.cathode, R7.Pin_1, TCRT3.connector3, TCRT4.connector3
  N1: LED1.anode, Componente2.D12/MISO
  N2: M1.pin_1, L298N.connector14
  N3: M1.pin_2, L298N.connector13
  N4: TCRT1.connector0, R13.Pin_0
  N5: TCRT1.connector2, R10.Pin_1
  VCC: ultasonoco.pin1, BT-06.VCC, Componente2.5V, U3.pin1, R3.P$1, R10.Pin_0, R11.Pin_1, R13.Pin_1, R14.Pin_0, R20.Pin_1, R2.P$2
  N6: ultasonoco.pin2, Componente2.D2
  N7: ultasonoco.pin3, Componente2.D3_PWM
  N8: BT-06.TXD, Componente2.D0/RX
  N9: BT-06.RXD, Componente2.D1/TX
  N10: Componente2.D8, L298N.connector7
  N11: Componente2.D9_PWM, L298N.connector6
  N12: Componente2.D10_PWM/SS, L298N.connector5
  N13: Componente2.D11_PWM/MOSI, L298N.connector4
  N14: Componente2.D13/SCK, LED.anode
  N15: Componente2.D4, U3.pin2
  N16: Componente2.D5_PWM, U3.pin3
  N17: Componente2.D6_PWM, L298N.connector9
  N18: Componente2.D7, L298N.connector8
  N19: U2.+, L298N.connector1
  N20: U2.-, L298N.connector2
  N21: L298N.connector10, M2.pin_2
  N22: L298N.connector11, M2.pin_1
  N23: TCRT2.connector0, R14.Pin_1
  N24: TCRT2.connector2, R11.Pin_0
  N25: R3.P$2, R7.Pin_0
  N26: R16.Pin_0, R2.P$1
  N27: TCRT3.connector0, R18.Pin_1
  N28: TCRT3.connector2, R19.Pin_1
  N29: TCRT4.connector0, R17.Pin_1
  N30: TCRT4.connector2, R20.Pin_0
