# Fritzing sketch id1127_4_Wire_Fan_0 (saved by Fritzing 0.9.2b)

parts:
  Onderdeel1 = Arduino Uno (Rev3)
  J1 = Screw terminal - 2 pins [package=THT]  # not connected
  R1 = Rotary Potentiometer (Small) [maximum_resistance=1kΩ package=THT]

nets:
  N1: Onderdeel1.A0, R1.wiper

notes:
  + 12 V Fan
  - 12 V Fan
  PWM Fan
  Sensor RPM
  Connect external Gnd. to Arduino Gnd.
  Fan : Nidec Betav TA350DC
