# Fritzing sketch id1129_nokia_5110_0 (saved by Fritzing 0.7.9b)
breadboards: 1

parts:
  Arduino1 = Arduino
  Nokia_5110_LCD_Module1 = Nokia5110LCDModule
  part = Zener Diode [part_number=1N4732A breakdown_voltage=3.6V package="300 mil [THT]"]  # not connected
  part_2 = 1k Ω Resistor [package=THT]  # not connected
  part_3 = 100 Ω Resistor [package=THT]  # not connected
  R1 = 47 Ω Resistor [package=THT]
  R2 = 47 Ω Resistor [package=THT]
  D1 = Rectifier Diode
  D2 = Rectifier Diode
  R3 = Trimmer Potentiometer [package=THT]
  R4 = 1k Ω Resistor [package=THT]

nets:
  N1: Arduino1.D7, Nokia_5110_LCD_Module1.connector1
  N2: Arduino1.D6, Nokia_5110_LCD_Module1.connector0
  N3: Arduino1.D5, Nokia_5110_LCD_Module1.connector2
  N4: Arduino1.D4, R2.Pin_1
  N5: Arduino1.D3, R1.Pin_1
  N6: Arduino1.+5V, R3.leg1, R4.Pin_1
  N7: Arduino1.GND, Nokia_5110_LCD_Module1.connector7, D1.connector1, D2.connector1, R3.leg2
  N8: Nokia_5110_LCD_Module1.connector3, R2.Pin_0, D2.connector0
  N9: Nokia_5110_LCD_Module1.connector4, R1.Pin_0, D1.connector0
  N10: Nokia_5110_LCD_Module1.connector5, R3.wiper
  N11: Nokia_5110_LCD_Module1.connector6, R4.Pin_0
