# Fritzing sketch id112_MyDiagram_0 (saved by Fritzing 0.9.1b)
breadboards: 1

parts:
  Part1 = Arduino Uno (Rev3)  # not connected
  R1 = Resistor [tolerance=±5% resistance=220 package="0603 [SMD]"]  # not connected
  R2 = Resistor [tolerance=±5% resistance=220 package="0603 [SMD]"]
  R3 = Resistor [tolerance=±5% resistance=220 package="0603 [SMD]"]
  LED1 = smd LED [color="Red (633nm)" package="0603 [SMD]"]  # not connected
  LED3 = smd LED [color="Red (633nm)" package="0603 [SMD]"]  # not connected
  LED4 = smd LED [color="Red (633nm)" package="0603 [SMD]"]  # not connected
  LED5 = smd LED [color="Red (633nm)" package="0603 [SMD]"]  # not connected
  LED6 = smd LED [color="Red (633nm)" package="0603 [SMD]"]  # not connected
  LED7 = smd LED [color="Red (633nm)" package="0603 [SMD]"]  # not connected
  LED8 = smd LED [color="Red (633nm)" package="0603 [SMD]"]  # not connected
  LED9 = smd LED [color="Red (633nm)" package="0603 [SMD]"]  # not connected
  LED10 = smd LED [color="Red (633nm)" package="0603 [SMD]"]  # not connected
  LED11 = smd LED [color="Red (633nm)" package="0603 [SMD]"]  # not connected
  LED12 = smd LED [color="Red (633nm)" package="0603 [SMD]"]  # not connected
  LED13 = smd LED [color="Red (633nm)" package="0603 [SMD]"]  # not connected
  LED14 = smd LED [color="Red (633nm)" package="0603 [SMD]"]  # not connected
  LED15 = smd LED [color="Red (633nm)" package="0603 [SMD]"]
  LED16 = smd LED [color="Red (633nm)" package="0603 [SMD]"]  # not connected
  LED17 = smd LED [color="Red (633nm)" package="0603 [SMD]"]  # not connected
  LED18 = smd LED [color="Red (633nm)" package="0603 [SMD]"]
  LED19 = smd LED [color="Red (633nm)" package="0603 [SMD]"]  # not connected
  LED20 = smd LED [color="Red (633nm)" package="0603 [SMD]"]  # not connected
  LED21 = smd LED [color="Red (633nm)" package="0603 [SMD]"]  # not connected
  LED22 = smd LED [color="Red (633nm)" package="0603 [SMD]"]  # not connected
  LED23 = smd LED [color="Red (633nm)" package="0603 [SMD]"]  # not connected
  LED24 = smd LED [color="Red (633nm)" package="0603 [SMD]"]
  LED25 = smd LED [color="Red (633nm)" package="0603 [SMD]"]  # not connected
  LED26 = smd LED [color="Red (633nm)" package="0603 [SMD]"]  # not connected
  LED27 = smd LED [color="Red (633nm)" package="0603 [SMD]"]
  LED28 = smd LED [color="Red (633nm)" package="0603 [SMD]"]  # not connected
  LED29 = smd LED [color="Red (633nm)" package="0603 [SMD]"]  # not connected
  LED30 = smd LED [color="Red (633nm)" package="0603 [SMD]"]  # not connected
  LED31 = smd LED [color="Red (633nm)" package="0603 [SMD]"]  # not connected
  LED32 = smd LED [color="Red (633nm)" package="0603 [SMD]"]  # not connected
  LED33 = smd LED [color="Red (633nm)" package="0603 [SMD]"]
  LED34 = smd LED [color="Red (633nm)" package="0603 [SMD]"]  # not connected
  LED35 = smd LED [color="Red (633nm)" package="0603 [SMD]"]  # not connected
  LED36 = smd LED [color="Red (633nm)" package="0603 [SMD]"]
  LED37 = smd LED [color="Red (633nm)" package="0603 [SMD]"]  # not connected
  LED38 = smd LED [color="Red (633nm)" package="0603 [SMD]"]  # not connected

nets:
  N1: R2.Pin_0, R3.Pin_0
  N2: LED15.cathode, LED18.cathode
  N3: LED24.cathode, LED27.cathode
  N4: LED33.cathode, LED36.cathode
