# Fritzing sketch id1131_connect_cds_led_0 (saved by Fritzing 0.9.3b)
breadboards: 1

parts:
  パーツ1 = Arduino Uno (Rev3)
  R1 = Resistor [tolerance=±5% resistance=180 package=THT]
  LED1 = LED - 5mm [color="Red (633nm)" package="5 mm [THT]"]
  R2 = Resistor [tolerance=±5% resistance=10k package=THT]
  R3 = Photocell (LDR) [package=THT]

nets:
  N1: パーツ1.A0, R2.Pin_0, R3.pin_1
  N2: パーツ1.D13/SCK, R1.Pin_0
  N3: パーツ1.GND, LED1.cathode, R2.Pin_1
  N4: パーツ1.5V, R3.pin_0
  N5: R1.Pin_1, LED1.anode
