# Fritzing sketch id1133_1_OKI_Stepper_Motor_model_MK17A4_0 (saved by Fritzing 0.9.2b)

parts:
  Part1 = Arduino Uno (Rev3)
  Part2 = EasyDriver_v44
  M1 = Stepper Motor - Bipolar

nets:
  GND: Part1.GND, Part2.GND
  N1: Part1.D2, Part2.DIR
  N2: Part1.D3_PWM, Part2.STEP
  N3: Part2.OUT2A, M1.B
  N4: Part2.OUT2B, M1.A
  N5: Part2.OUT1A, M1.C
  N6: Part2.OUT1B, M1.D
