# Fritzing sketch id1134_conectar_un_lcd_yb2004a_y_un_mp3_shield_de_sparkfun_a_un_arduino_uno_r2_0 (saved by Fritzing 0.7.1b)
breadboards: 1

parts:
  Arduino1 = Arduino  # not connected
  Parte1 = Arduino MP3 Player Shield
  LCD1 = LCD screen
  R1 = Rotary Potentiometer (Small) [maximum_resistance=10kΩ]

nets:
  VCC: Parte1.VCC, LCD1.VDD, LCD1.LED+
  N1: Parte1.5V-MIDI-RX, LCD1.DB6
  N2: Parte1.5V-GPIO1, LCD1.DB5
  N3: Parte1.D5, LCD1.DB4
  N4: Parte1.5V-MOSI, LCD1.E, LCD1.DB0
  N5: Parte1.MISO, LCD1.RS
  GND: Parte1.GND, LCD1.VSS, LCD1.R/W, LCD1.LED-, R1.leg1, R1.leg2
  N6: Parte1.TX, LCD1.DB7
