# Fritzing sketch id1135_cancello_schema_0 (saved by Fritzing 0.9.3b)
breadboards: 1

parts:
  Componente1 = Arduino Uno (Rev3)
  Q1 = NPN-Transistor [package="TO92 [THT]"]
  R1 = resistor 1k
  U1 = RELAY [package=relay-g5q]
  D1 = Schottky Diode [part_number=1N5817 package="Melf DO-213 AB [SMD]"]

nets:
  N1: Componente1.D8, R1.connector1
  N2: Componente1.5V, U1.COIL2, D1.cathode
  N3: Componente1.GND, Q1.C
  N4: Q1.E, U1.NO, D1.anode
  N5: Q1.B, R1.connector0
