# Fritzing sketch id1136_sk_0 (saved by Fritzing 0.9.3b)
circuit board: 6.33387cm x 3.04003cm
breadboards: 1

parts:
  R1 = Resistor [tolerance=±5% resistance=220 package=THT]
  R3 = Resistor [tolerance=±5% resistance=220 package=THT]
  R4 = Resistor [tolerance=±5% resistance=220 package=THT]
  R5 = Resistor [tolerance=±5% resistance=220 package=THT]
  R6 = Resistor [tolerance=±5% resistance=220 package=THT]
  J1 = Screw terminal - 2 pins [package=THT]
  J2 = Screw terminal - 2 pins [package=THT]
  J3 = Screw terminal - 2 pins [package=THT]
  J4 = Screw terminal - 2 pins [package=THT]
  J5 = Screw terminal - 2 pins [package=THT]
  J6 = Screw terminal - 2 pins [package=THT]
  R7 = Resistor [tolerance=±5% resistance=220 package=THT]
  J7 = Screw terminal - 2 pins [package=THT]
  J8 = Screw terminal - 2 pins [package=THT]
  J9 = Screw terminal - 2 pins [package=THT]
  J10 = Screw terminal - 2 pins [package=THT]
  J11 = Screw terminal - 2 pins [package=THT]
  J12 = Screw terminal - 2 pins [package=THT]

nets:
  N1: R1.Pin_0, J12.pin2
  N2: R1.Pin_1, J1.pin2
  N3: R3.Pin_0, J7.pin2
  N4: R3.Pin_1, J3.pin2
  N5: R4.Pin_0, J9.pin2
  N6: R4.Pin_1, J6.pin2
  N7: R5.Pin_0, J11.pin2
  N8: R5.Pin_1, J4.pin2
  N9: R6.Pin_0, J10.pin2
  N10: R6.Pin_1, J5.pin2
  N11: J1.pin1, J12.pin1
  N12: J2.pin1, J8.pin1
  N13: J2.pin2, R7.Pin_1
  N14: J3.pin1, J7.pin1
  N15: J4.pin1, J11.pin1
  N16: J5.pin1, J10.pin1
  N17: J6.pin1, J9.pin1
  N18: R7.Pin_0, J8.pin2

notes:
  Muerzo Web Creation
