# Fritzing sketch id1137_constant_load_0 (saved by Fritzing 0.9.3b)
breadboards: 1

parts:
  J1 = Screw terminal - 2 pins [package=THT]
  J2 = Screw terminal - 2 pins [package=THT]
  R1 = Trimmer Potentiometer [maximum_resistance=0.5MΩ package=THT]
  R2 = Trimmer Potentiometer [maximum_resistance=0.5MΩ package=THT]
  Q2 = MOSFET-NCHANNEL [package=to220v]
  R3 = Resistor [tolerance=±5% resistance=1 package=THT]
  U1 = LM 358 Dual Op-Amp [package="SO 08 [SMD]"]
  Q1 = MOSFET-NCHANNEL [package=to220v]

nets:
  6V: J1.pin1, R1.leg2, R2.leg2, U1.connector7
  GND: J1.pin2, J2.pin2, R1.leg1, R2.leg1, R3.Pin_1, U1.connector3, Q1.S
  N1: J2.pin1, Q2.D, U1.connector1
  N2: R1.wiper, U1.connector2
  N3: R2.wiper, U1.connector4, Q1.D
  N4: Q2.G, U1.connector6
  N5: Q2.S, R3.Pin_0, U1.connector5
  N6: U1.connector0, Q1.G

notes:
  battery
  power supply
  current op-amp
  voltage op-amp
  R1 -> 3V to op-amp +
  R2 -> current to op-amp +
