# Fritzing sketch id113_FritzCube2_0 (saved by Fritzing 0.7.5b)
breadboards: 4

parts:
  U1 = atmega328 [package=dip]
  LED37 = LED - 3mm [color="Red (635nm)" package="3 mm [THT]"]
  LED38 = LED - 3mm [color="Red (635nm)" package="3 mm [THT]"]
  LED39 = LED - 3mm [color="Red (635nm)" package="3 mm [THT]"]
  LED40 = LED - 3mm [color="Red (635nm)" package="3 mm [THT]"]
  LED41 = LED - 3mm [color="Red (635nm)" package="3 mm [THT]"]
  LED42 = LED - 3mm [color="Red (635nm)" package="3 mm [THT]"]
  LED43 = LED - 3mm [color="Red (635nm)" package="3 mm [THT]"]
  LED44 = LED - 3mm [color="Red (635nm)" package="3 mm [THT]"]
  LED45 = LED - 3mm [color="Red (635nm)" package="3 mm [THT]"]
  R1 = Resistor [tolerance=±5% resistance=22k package=THT]
  R2 = Resistor [tolerance=±5% resistance=22k package=THT]
  R3 = Resistor [tolerance=±5% resistance=22k package=THT]
  R4 = Resistor [tolerance=±5% resistance=22k package=THT]
  R5 = Resistor [tolerance=±5% resistance=22k package=THT]
  R7 = Resistor [tolerance=±5% resistance=22k package=THT]
  R8 = Resistor [tolerance=±5% resistance=22k package=THT]
  R9 = Resistor [tolerance=±5% resistance=22k package=THT]
  R10 = Resistor [tolerance=±5% resistance=220 package=THT]
  R11 = Resistor [tolerance=±5% resistance=220 package=THT]
  R12 = Resistor [tolerance=±5% resistance=220 package=THT]
  XTAL1 = Crystal [frequency="16 Mhz" package=THT]
  C1 = Ceramic Capacitor [capacitance=0.22mF package="100 mil [THT, multilayer]"]
  C2 = Ceramic Capacitor [capacitance=0.22mF package="100 mil [THT, multilayer]"]
  U2 = Voltage Regulator - 5V [package="TO220 [THT]"]
  C3 = Electrolytic Capacitor [capacitance=10µF voltage=50V package="100 mil [THT, electrolytic]"]
  C4 = Electrolytic Capacitor [capacitance=10µF voltage=50V package="100 mil [THT, electrolytic]"]
  R13 = Resistor [tolerance=±5% resistance=1k package=THT]
  R14 = Resistor [tolerance=±5% resistance=10k package=THT]
  R15 = Resistor [tolerance=±5% resistance=22k package=THT]
  S1 = Pushbutton [package="[THT]"]
  LED64 = LED - 3mm [color="Blue (430nm)" package="3 mm [THT]"]
  Q1 = NPN-Transistor [package="TO92 [THT]"]
  Q2 = NPN-Transistor [package="TO92 [THT]"]
  Q3 = NPN-Transistor [package="TO92 [THT]"]
  LED83 = LED - 3mm [color="Yellow (595nm)" package="3 mm [THT]"]
  LED84 = LED - 3mm [color="Red (635nm)" package="3 mm [THT]"]
  LED85 = LED - 3mm [color="Yellow (595nm)" package="3 mm [THT]"]
  LED86 = LED - 3mm [color="Red (635nm)" package="3 mm [THT]"]
  LED87 = LED - 3mm [color="Yellow (595nm)" package="3 mm [THT]"]
  LED88 = LED - 3mm [color="Red (635nm)" package="3 mm [THT]"]
  LED89 = LED - 3mm [color="Yellow (595nm)" package="3 mm [THT]"]
  LED90 = LED - 3mm [color="Red (635nm)" package="3 mm [THT]"]
  LED91 = LED - 3mm [color="Yellow (595nm)" package="3 mm [THT]"]
  LED92 = LED - 3mm [color="Red (635nm)" package="3 mm [THT]"]
  LED93 = LED - 3mm [color="Yellow (595nm)" package="3 mm [THT]"]
  LED94 = LED - 3mm [color="Red (635nm)" package="3 mm [THT]"]
  LED95 = LED - 3mm [color="Yellow (595nm)" package="3 mm [THT]"]
  LED96 = LED - 3mm [color="Red (635nm)" package="3 mm [THT]"]
  LED97 = LED - 3mm [color="Yellow (595nm)" package="3 mm [THT]"]
  LED98 = LED - 3mm [color="Red (635nm)" package="3 mm [THT]"]
  LED99 = LED - 3mm [color="Yellow (595nm)" package="3 mm [THT]"]
  LED100 = LED - 3mm [color="Red (635nm)" package="3 mm [THT]"]

nets:
  N1: U1.RESET, R14.Pin_1, S1.Pin_1, S1.Pin_2
  N2: U1.D2, R1.Pin_1
  N3: U1.D3_(PWM), R9.Pin_1
  N4: U1.D4, R8.Pin_1
  N5: U1.VCC, U1.AVCC, U1.AREF, C1.0, C2.0, U2.output_voltage, C4.+, R14.Pin_0, LED64.anode
  GND: U1.GND, U2.GND, C3.-, C4.-, R13.Pin_0, S1.Pin_3, S1.Pin_4, Q1.E, Q2.E, Q3.E
  N6: U1.XLAT1, XTAL1.pin_1, C1.1
  N7: U1.XLAT2, XTAL1.pin_0, C2.1
  N8: U1.D5_(PWM), R2.Pin_1
  N9: U1.D6_(PWM), R7.Pin_1
  N10: U1.D7, R15.Pin_1
  N11: U1.D8, R3.Pin_1
  N12: U1.D9_(PWM), R5.Pin_1
  N13: U1.D10_(PWM), R4.Pin_1
  N14: U1.D11_(PWM), R11.Pin_1
  N15: U1.D12, R12.Pin_1
  N16: U1.D13, R10.Pin_1
  N17: LED37.cathode, R2.Pin_0
  N18: LED37.anode, LED38.anode, LED39.anode, LED40.anode, LED41.anode, LED42.anode, LED43.anode, LED44.anode, LED45.anode, Q3.C
  N19: LED38.cathode, R9.Pin_0
  N20: LED39.cathode, R1.Pin_0
  N21: LED40.cathode, R7.Pin_0
  N22: LED41.cathode, R8.Pin_0
  N23: LED42.cathode, R15.Pin_0
  N24: LED43.cathode, R3.Pin_0
  N25: LED44.cathode, R5.Pin_0
  N26: LED45.cathode, R4.Pin_0
  N27: R10.Pin_0, Q1.B
  N28: R11.Pin_0, Q3.B
  N29: R12.Pin_0, Q2.B
  N30: U2.input_voltage, C3.+
  N31: R13.Pin_1, LED64.cathode
  N32: LED83.cathode, LED84.cathode
  N33: LED83.anode, LED85.anode, LED87.anode, LED89.anode, LED91.anode, LED93.anode, LED95.anode, LED97.anode, LED99.anode
  N34: LED84.anode, LED86.anode, LED88.anode, LED90.anode, LED92.anode, LED94.anode, LED96.anode, LED98.anode, LED100.anode
  N35: LED85.cathode, LED86.cathode
  N36: LED87.cathode, LED88.cathode
  N37: LED89.cathode, LED90.cathode
  N38: LED91.cathode, LED92.cathode
  N39: LED93.cathode, LED94.cathode
  N40: LED95.cathode, LED96.cathode
  N41: LED97.cathode, LED98.cathode
  N42: LED99.cathode, LED100.cathode

notes:
  [1-1 to D10]
  [1-2 to D9]
  [1-3 to D8]
  [1-4 to D7]
  [1-5 to D6]
  [1-6 to D5]
  [1-7 to D4]
  [1-8 to D3]
  [1-9 to D2]
