# Fritzing sketch id1142_Canon_CIS_Sensor_Sketch_0 (saved by Fritzing 0.9.3b)
breadboards: 1

parts:
  Bauteil1 = Arduino Uno (Rev3)
  R1 = Resistor [tolerance=±5% resistance=220 package=THT]
  R2 = Resistor [tolerance=±5% resistance=220 package=THT]
  R3 = Resistor [tolerance=±5% resistance=220 package=THT]
  R4 = Resistor [tolerance=±5% resistance=10k package=THT]
  R5 = Resistor [tolerance=±5% resistance=10k package=THT]
  R6 = Resistor [tolerance=±5% resistance=1k package=THT]
  R7 = Resistor [tolerance=±5% resistance=1.2k package=THT]
  R8 = Resistor [tolerance=±5% resistance=2.2k package=THT]
  J1 = female pin header, 12 pins [form="♀ (female)"]

nets:
  N1: Bauteil1.A0, J1.pin7
  N2: Bauteil1.A1, J1.pin6
  N3: Bauteil1.A4/SDA, R6.Pin_0
  N4: Bauteil1.D5_PWM, R3.Pin_1
  N5: Bauteil1.D6_PWM, R2.Pin_1
  N6: Bauteil1.D7, R1.Pin_1
  N7: Bauteil1.3V3, R5.Pin_0, R8.Pin_0, J1.pin4, J1.pin12
  N8: Bauteil1.GND, R4.Pin_1, R7.Pin_1, J1.pin3, J1.pin5, J1.pin8
  N9: R1.Pin_0, J1.pin11
  N10: R2.Pin_0, J1.pin10
  N11: R3.Pin_0, J1.pin9
  N12: R4.Pin_0, R5.Pin_1, R6.Pin_1, J1.pin1
  N13: R7.Pin_0, R8.Pin_1, J1.pin2

notes:
  1
  12
  CIS-Sensor
  Analog Signal
  Start Pulse
  Clock
