# Fritzing sketch id1143_AC_detector_0 (saved by Fritzing 0.9.2b)
circuit board: 8.46667cm x 5.64444cm
breadboards: 1

parts:
  CD4017 = CD4048B [part_number=CD4017 package="DIP (Dual Inline) [THT]"]
  Power_plug1 = Power plug
  C1 = Ceramic Capacitor [capacitance=100nF package="100 mil [THT, multilayer]"]
  ANT1 = Antenna
  R1 = Resistor [tolerance=±5% resistance=100 package=THT]
  LED1 = LED - 5mm [color="Red (633nm)" package="5 mm [THT]"]

nets:
  N1: CD4017.H, R1.Pin_1
  GND: CD4017.VSS, CD4017.B, CD4017.EXPAND, Power_plug1.GND, C1.0, C1.1, LED1.cathode
  N2: CD4017.A, ANT1.antenna_lead
  VDD: CD4017.VDD, Power_plug1.VCC
  N3: R1.Pin_0, LED1.anode
