# Fritzing sketch id1145_Untitled_Sketch_0 (saved by Fritzing 0.9.2b)
circuit board: 8.46667cm x 5.64444cm
breadboards: 1

parts:
  7_Segment2 = 7 Segment Display
  7_Segment1 = 7 Segment Display
  Q1 = NPN-Transistor [package="TO92 [THT]"]
  R1 = Resistor [tolerance=±5% resistance=470 package=THT]
  R2 = Resistor [tolerance=±5% resistance=1k package=THT]
  R3 = Resistor [tolerance=±5% resistance=470 package=THT]
  R4 = Resistor [tolerance=±5% resistance=470 package=THT]
  R5 = Resistor [tolerance=±5% resistance=470 package=THT]
  Q2 = NPN-Transistor [package="TO92 [THT]"]
  R6 = Resistor [tolerance=±5% resistance=1k package=THT]
  Componente1 = Arduino Uno (Rev3)
  R7 = Photocell (LDR) [package=THT]
  R8 = Resistor [tolerance=±5% resistance=1k package=THT]

nets:
  N1: 7_Segment2.common_anode, R4.Pin_0, R5.Pin_0
  N2: 7_Segment1.Segment_E, Componente1.D7
  N3: 7_Segment1.Segment_D, Componente1.D6_PWM
  N4: 7_Segment1.common_anode, R1.Pin_1, R3.Pin_1
  N5: 7_Segment1.Segment_C, Componente1.D5_PWM
  N6: 7_Segment1.Segment_DP, Componente1.D10_PWM/SS
  N7: 7_Segment1.Segment_B, Componente1.D4
  N8: 7_Segment1.Segment_A, Componente1.D3_PWM
  N9: 7_Segment1.Segment_F, Componente1.D8
  N10: 7_Segment1.Segment_G, Componente1.D9_PWM
  N11: Q1.E, Q2.E, Componente1.GND, R8.Pin_1
  N12: Q1.B, R2.Pin_0
  N13: Q1.C, R1.Pin_0, R3.Pin_0
  N14: R2.Pin_1, Componente1.D11_PWM/MOSI
  N15: R4.Pin_1, R5.Pin_1, Q2.C
  N16: Q2.B, R6.Pin_1
  N17: R6.Pin_0, Componente1.D12/MISO
  N18: Componente1.D2, R7.pin_1, R8.Pin_0
  N19: Componente1.5V, R7.pin_0
