# Fritzing sketch id1147_Decodificador_7447_0 (saved by Fritzing 0.9.2b)
circuit board: 8.46667cm x 5.64444cm
breadboards: 1

parts:
  Parte1 = Arduino Uno (Rev3)
  U2 = SN74LS47N
  DI1-U = 7-Segment LED Display [package=THT]
  DI2-D = 7-Segment LED Display [package=THT]
  R2 = Resistor [tolerance=±5% resistance=330 package=THT]
  R1 = Resistor [tolerance=±5% resistance=330 package=THT]
  U1 = SN74LS47N

nets:
  N1: Parte1.D8, U1.connector1
  N2: Parte1.D9_PWM, U1.connector5
  N3: Parte1.D10_PWM/SS, U2.connector6
  N4: Parte1.D11_PWM/MOSI, U2.connector0
  N5: Parte1.D12/MISO, U2.connector1
  N6: Parte1.D13/SCK, U2.connector5
  N7: Parte1.GND, U2.connector7, U1.connector7
  N8: Parte1.D6_PWM, U1.connector6
  N9: Parte1.D7, U1.connector0
  N10: Parte1.5V, U2.connector15, R2.Pin_0, R1.Pin_0, U1.connector15
  N11: U2.connector8, DI2-D.cathodeE
  N12: U2.connector9, DI2-D.cathodeD
  N13: U2.connector10, DI2-D.cathodeC
  N14: U2.connector11, DI2-D.cathodeB
  N15: U2.connector12, DI2-D.cathodeA
  N16: U2.connector13, DI2-D.cathodeG
  N17: U2.connector14, DI2-D.cathodeF
  N18: DI1-U.cathodeE, U1.connector8
  N19: DI1-U.cathodeD, U1.connector9
  N20: DI1-U.cathodeC, U1.connector10
  N21: DI1-U.cathodeB, U1.connector11
  N22: DI1-U.cathodeA, U1.connector12
  N23: DI1-U.commAnode#7, R1.Pin_1
  N24: DI1-U.cathodeF, U1.connector14
  N25: DI1-U.cathodeG, U1.connector13
  N26: DI2-D.commAnode#7, R2.Pin_1
