# Fritzing sketch id1148_CONTADOR_BINARIO_9_BIT_PARA_PLL_0 (saved by Fritzing 0.9.0b)
breadboards: 1

parts:
  Parte1 = Arduino Uno (Rev3)
  S1 = Momentary Switch [package=ksa_sealed_tac_switch]
  LED1 = LED - 5mm [color="Red (633nm)" package="5 mm [THT]"]
  LED2 = LED - 5mm [color="Red (633nm)" package="5 mm [THT]"]
  LED3 = LED - 5mm [color="Red (633nm)" package="5 mm [THT]"]
  LED4 = LED - 5mm [color="Red (633nm)" package="5 mm [THT]"]
  LED5 = LED - 5mm [color="Red (633nm)" package="5 mm [THT]"]
  LED6 = LED - 5mm [color="Red (633nm)" package="5 mm [THT]"]
  LED7 = LED - 5mm [color="Red (633nm)" package="5 mm [THT]"]
  LED8 = LED - 5mm [color="Red (633nm)" package="5 mm [THT]"]
  LED9 = LED - 5mm [color="Red (633nm)" package="5 mm [THT]"]
  R1 = Resistor [tolerance=±5% resistance=220 package=THT]
  R2 = Resistor [tolerance=±5% resistance=220 package=THT]
  R3 = Resistor [tolerance=±5% resistance=220 package=THT]
  R4 = Resistor [tolerance=±5% resistance=220 package=THT]
  R5 = Resistor [tolerance=±5% resistance=220 package=THT]
  R6 = Resistor [tolerance=±5% resistance=220 package=THT]
  R7 = Resistor [tolerance=±5% resistance=220 package=THT]
  R8 = Resistor [tolerance=±5% resistance=220 package=THT]
  R9 = Resistor [tolerance=±5% resistance=220 package=THT]
  R10 = Resistor [tolerance=±5% resistance=220 package=THT]

nets:
  N1: Parte1.D8, R4.Pin_1
  N2: Parte1.D9_PWM, R5.Pin_1
  N3: Parte1.D10_PWM/SS, R6.Pin_1
  N4: Parte1.D11_PWM/MOSI, R7.Pin_1
  N5: Parte1.D12/MISO, R8.Pin_1
  N6: Parte1.D13/SCK, R9.Pin_1
  N7: Parte1.GND, S1.2, S1.4, LED1.cathode, LED2.cathode, LED3.cathode, LED4.cathode, LED5.cathode, LED6.cathode, LED7.cathode, LED8.cathode, LED9.cathode
  N8: Parte1.D2, S1.1, S1.3, R10.Pin_0
  N9: Parte1.D5_PWM, R1.Pin_1
  N10: Parte1.D6_PWM, R2.Pin_1
  N11: Parte1.D7, R3.Pin_1
  N12: Parte1.5V, R10.Pin_1
  N13: LED1.anode, R1.Pin_0
  N14: LED2.anode, R2.Pin_0
  N15: LED3.anode, R3.Pin_0
  N16: LED4.anode, R4.Pin_0
  N17: LED5.anode, R5.Pin_0
  N18: LED6.anode, R6.Pin_0
  N19: LED7.anode, R7.Pin_0
  N20: LED8.anode, R8.Pin_0
  N21: LED9.anode, R9.Pin_0
