# Fritzing sketch id1149_Dos_displays_7_segmentos_0 (saved by Fritzing 0.8.7b)
breadboards: 2

parts:
  Parte1 = Arduino Uno (Rev3) - ICSP
  7_Segment1 = 7 Segment Display
  7_Segment2 = 7 Segment Display
  R1 = Resistor [tolerance=±5% resistance=330 package=THT]
  R2 = Resistor [tolerance=±5% resistance=330 package=THT]
  R3 = Resistor [tolerance=±5% resistance=330 package=THT]
  R4 = Resistor [tolerance=±5% resistance=330 package=THT]
  R5 = Resistor [tolerance=±5% resistance=330 package=THT]
  R6 = Resistor [tolerance=±5% resistance=330 package=THT]
  R7 = Resistor [tolerance=±5% resistance=330 package=THT]
  R8 = Resistor [tolerance=±5% resistance=330 package=THT]
  R9 = Resistor [tolerance=±5% resistance=330 package=THT]
  R10 = Resistor [tolerance=±5% resistance=330 package=THT]
  R11 = Resistor [tolerance=±5% resistance=330 package=THT]
  R12 = Resistor [tolerance=±5% resistance=330 package=THT]
  R13 = Resistor [tolerance=±5% resistance=330 package=THT]
  R14 = Resistor [tolerance=±5% resistance=330 package=THT]
  R15 = Resistor [tolerance=±5% resistance=330 package=THT]
  R16 = Resistor [tolerance=±5% resistance=330 package=THT]

nets:
  N1: Parte1.A4/SDA, R16.Pin_0
  N2: Parte1.A5/SCL, R13.Pin_0
  N3: Parte1.D8, R10.Pin_0
  N4: Parte1.D9_PWM, R9.Pin_0
  N5: Parte1.D10_PWM/SS, R14.Pin_0
  N6: Parte1.D11_PWM/MOSI, R11.Pin_0
  N7: Parte1.D12/MISO, R15.Pin_0
  N8: Parte1.D13/SCK, R12.Pin_0
  N9: Parte1.D0/RX, R1.Pin_0
  N10: Parte1.D1/TX, R2.Pin_0
  N11: Parte1.D2, R4.Pin_0
  N12: Parte1.D3_PWM, R3.Pin_0
  N13: Parte1.D4, R5.Pin_0
  N14: Parte1.D5_PWM, R6.Pin_0
  N15: Parte1.D6_PWM, R7.Pin_0
  N16: Parte1.D7, R8.Pin_0
  N17: Parte1.GND, 7_Segment1.Segment_A#1, 7_Segment2.Segment_A#1
  N18: 7_Segment1.common_cathode#3, R2.Pin_1
  N19: 7_Segment1.Segment_E, R4.Pin_1
  N20: 7_Segment1.Segment_D, R3.Pin_1
  N21: 7_Segment1.Segment_C, R5.Pin_1
  N22: 7_Segment1.common_cathode#8, R6.Pin_1
  N23: 7_Segment1.Segment_B, R7.Pin_1
  N24: 7_Segment1.Segment_A#10, R8.Pin_1
  N25: 7_Segment2.Segment_F, R10.Pin_1
  N26: 7_Segment2.common_cathode#3, R9.Pin_1
  N27: 7_Segment2.Segment_E, R14.Pin_1
  N28: 7_Segment2.Segment_D, R11.Pin_1
  N29: 7_Segment2.Segment_C, R15.Pin_1
  N30: 7_Segment2.common_cathode#8, R12.Pin_1
  N31: 7_Segment2.Segment_B, R13.Pin_1
  N32: 7_Segment2.Segment_A#10, R16.Pin_1

notes:
  Contador con dos displays de 7 segmentos
