# Fritzing sketch id1153_Untitled_Sketch_0 (saved by Fritzing 0.7.12b)
breadboards: 1

parts:
  Arduino1 = Arduino
  J1 = Basic Servo
  J2 = Basic Servo

nets:
  N1: Arduino1.D9, J1.pulse
  N2: Arduino1.D3, J2.pulse
  VCC: Arduino1.+5V, J1.vcc, J2.vcc
  GND: Arduino1.GND, J1.gnd, J2.gnd
