# Fritzing sketch id1154_contrinex01_0 (saved by Fritzing 0.9.2b)
circuit board: 8.46667cm x 5.64444cm

parts:
  Arduino = Arduino Uno (Rev3)
  RS485 = RS485 [package=so08]
  Power_24V = Power plug
  J1 = female pin header, 2 pins [form="♀ (female)"]
  J2 = female pin header, 2 pins [form="♀ (female)"]
  LED1 = LED - 5mm [color="Red (633nm)" package="5 mm [THT]"]
  LED2 = LED - 5mm [color="Red (633nm)" package="5 mm [THT]"]
  LED3 = LED - 5mm [color="Red (633nm)" package="5 mm [THT]"]
  LED4 = LED - 5mm [color="Red (633nm)" package="5 mm [THT]"]
  LED5 = LED - 5mm [color="Red (633nm)" package="5 mm [THT]"]
  LED6 = LED - 5mm [color="Red (633nm)" package="5 mm [THT]"]
  LED7 = LED - 5mm [color="Red (633nm)" package="5 mm [THT]"]
  LED8 = LED - 5mm [color="Red (633nm)" package="5 mm [THT]"]
  R1 = Resistor [tolerance=±5% resistance=330 package=THT]
  R2 = Resistor [tolerance=±5% resistance=330 package=THT]
  R3 = Resistor [tolerance=±5% resistance=330 package=THT]
  R4 = Resistor [tolerance=±5% resistance=330 package=THT]
  R5 = Resistor [tolerance=±5% resistance=330 package=THT]
  R6 = Resistor [tolerance=±5% resistance=330 package=THT]
  R7 = Resistor [tolerance=±5% resistance=330 package=THT]
  R8 = Resistor [tolerance=±5% resistance=330 package=THT]

nets:
  N1: Arduino.D8, R6.Pin_1
  N2: Arduino.D9_PWM, R5.Pin_1
  N3: Arduino.D10_PWM/SS, R4.Pin_1
  N4: Arduino.D11_PWM/MOSI, R3.Pin_1
  N5: Arduino.D12/MISO, R2.Pin_1
  N6: Arduino.D13/SCK, R1.Pin_1
  GND: Arduino.GND, RS485.GND, Power_24V.GND, J1.pin2, LED1.cathode, LED2.cathode, LED3.cathode, LED4.cathode, LED5.cathode, LED6.cathode, LED7.cathode, LED8.cathode
  N7: Arduino.D0/RX, RS485.RO
  N8: Arduino.D1/TX, RS485.DI
  N9: Arduino.D2, RS485._RE, RS485.DE
  N10: Arduino.D6_PWM, R8.Pin_1
  N11: Arduino.D7, R7.Pin_1
  5V: Arduino.5V, RS485.VCC
  N12: RS485.A, J2.pin2
  N13: RS485.B, J1.pin1
  N14: Power_24V.VCC, J2.pin1
  N15: LED1.anode, R2.Pin_0
  N16: LED2.anode, R3.Pin_0
  N17: LED3.anode, R4.Pin_0
  N18: LED4.anode, R5.Pin_0
  N19: LED5.anode, R6.Pin_0
  N20: LED6.anode, R7.Pin_0
  N21: LED7.anode, R8.Pin_0
  N22: LED8.anode, R1.Pin_0

notes:
  CONTRINEX RLS-1183-020
  24v
  RS485
