# Fritzing sketch id1155_schema_led_0 (saved by Fritzing 0.8.6b)
breadboards: 1

parts:
  Componente1 = Arduino Mega 2560 (Rev3)  # not connected
  Componente2 = Arduino Ethernet Shield (Rev3)
  R1 = Resistor [tolerance=±5% resistance=220 package=THT]
  LED1 = LED - 5mm [color="Red (633nm)" package="5 mm [THT]"]
  R2 = Resistor [tolerance=±5% resistance=220 package=THT]
  LED2 = LED - 5mm [color="Green (555nm)" package="5 mm [THT]"]

nets:
  N1: Componente2.GND, LED1.anode, LED2.anode
  N2: Componente2.D2, R1.Pin_0
  N3: Componente2.PWM_D3, R2.Pin_0
  N4: R1.Pin_1, LED1.cathode
  N5: R2.Pin_1, LED2.cathode
