# Fritzing sketch id1157_rfid_rc522_0 (saved by Fritzing 0.9.3b)
circuit board: 8.46667cm x 5.64444cm
breadboards: 1

parts:
  Componente1 = RFID-RC522
  LCD1 = LCD screen
  Componente2 = Arduino Mega 2560 (Rev3)
  R1 = Rotary Potentiometer (Small) [maximum_resistance=100kΩ package=THT]
  LED1 = DUO LED RG [package="5 mm [THT]"]
  R2 = Resistor [tolerance=±5% resistance=220 package=THT]

nets:
  N1: Componente1.connector8, Componente2.D53
  N2: Componente1.connector9, Componente2.D52
  N3: Componente1.connector10, Componente2.D51
  N4: Componente1.connector11, Componente2.D50
  VSS: Componente1.connector13, LCD1.VSS, LCD1.R/W, LCD1.LED-, Componente2.GND, R1.leg1, R2.Pin_0
  N5: Componente1.connector14, Componente2.D6_PWM
  N6: Componente1.connector15, Componente2.3V3
  VDD: LCD1.VDD, LCD1.LED+, Componente2.5V, R1.leg2
  N7: LCD1.V0, R1.wiper
  N8: LCD1.RS, Componente2.D12_PWM
  N9: LCD1.E, Componente2.D11_PWM
  N10: LCD1.DB4, Componente2.D5_PWM
  N11: LCD1.DB5, Componente2.D4_PWM
  N12: LCD1.DB6, Componente2.D3_PWM
  N13: LCD1.DB7, Componente2.D2_PWM
  N14: Componente2.D8_PWM, LED1.red_anode
  N15: Componente2.D7_PWM, LED1.green_anode
  N16: LED1.common_cathode, R2.Pin_1
