# Fritzing sketch id1158_Raspberry_PI_PCF8574_0 (saved by Fritzing 0.9.3b)
breadboards: 1

parts:
  Raspberry_Pi_1 = Raspberry Pi 3 [part_number=RPI-3-V1.2]
  U1 = PCF8574 [package="DIP16 [THT]"]
  8_Channel_Relay1 = richardbruneau00

nets:
  3V3: Raspberry_Pi_1.3v3, Raspberry_Pi_1.3V3, U1.VCC
  N1: Raspberry_Pi_1.GPIO2, U1.SDA
  N2: Raspberry_Pi_1.GPIO3, U1.SCL
  GND: Raspberry_Pi_1.GND, U1.A0, U1.A1, U1.A3, U1.GND, 8_Channel_Relay1.connector8
  N3: Raspberry_Pi_1.5V, 8_Channel_Relay1.connector17
  N4: U1.P0, 8_Channel_Relay1.connector9
  N5: U1.P1, 8_Channel_Relay1.connector10
  N6: U1.P2, 8_Channel_Relay1.connector11
  N7: U1.P3, 8_Channel_Relay1.connector12
  N8: U1.P4, 8_Channel_Relay1.connector13
  N9: U1.P5, 8_Channel_Relay1.connector14
  N10: U1.P6, 8_Channel_Relay1.connector15
  N11: U1.P7, 8_Channel_Relay1.connector16
