# Fritzing sketch id1159_control_motor_with_bluetooth_0 (saved by Fritzing 0.9.0b)
breadboards: 1

parts:
  Part1 = Arduino Uno (Rev3)
  IC1 = IC, DIP package, 16 pins [chip_label="IC L293D"]
  M1 = DC Motor

nets:
  N1: Part1.GND, IC1.pin4, IC1.pin5, IC1.pin13, IC1.pin14
  N2: Part1.D3_PWM, IC1.pin7
  N3: Part1.D4, IC1.pin2
  N4: Part1.D5_PWM, IC1.pin1
  N5: Part1.3V3, IC1.pin8, IC1.pin16
  N6: IC1.pin3, M1.pin_2
  N7: IC1.pin6, M1.pin_1

notes:
  Bluetooth Module
  HC-05
  VCC
  GND
  TXD
  RXD
