# Fritzing sketch id115_pushbtn_0 (saved by Fritzing 0.9.2b)
breadboards: 1

parts:
  元件1 = Arduino Uno (Rev3)
  LED1 = LED - 5mm [color="Red (633nm)" package="5 mm [THT]"]
  R1 = Resistor [tolerance=±5% resistance=10k package=THT]
  S1 = Pushbutton [package="[THT]"]

nets:
  N1: 元件1.D13/SCK, LED1.anode
  N2: 元件1.GND, LED1.cathode, R1.Pin_0
  N3: 元件1.D2, R1.Pin_1, S1.Pin_3, S1.Pin_4
  N4: 元件1.5V, S1.Pin_1, S1.Pin_2
