# Fritzing sketch id1160_display_0 (saved by Fritzing 0.7.10b)
breadboards: 1

parts:
  Q1 = NPN-Transistor [package="TO92 [THT]"]
  Q2 = NPN-Transistor [package="TO92 [THT]"]
  R2 = Resistor [tolerance=±5% resistance=220 package=THT]
  R3 = Resistor [tolerance=±5% resistance=220 package=THT]
  R4 = Resistor [tolerance=±5% resistance=220 package=THT]
  R5 = Resistor [tolerance=±5% resistance=220 package=THT]
  R6 = Resistor [tolerance=±5% resistance=220 package=THT]
  R7 = Resistor [tolerance=±5% resistance=220 package=THT]
  R8 = Resistor [tolerance=±5% resistance=220 package=THT]
  R9 = Resistor [tolerance=±5% resistance=3.9k package=THT]
  R10 = Resistor [tolerance=±5% resistance=3.9k package=THT]
  Arduino1 = Arduino
  7_Segment1 = 7 Segment Display
  7_Segment2 = 7 Segment Display

nets:
  N1: Q1.E, Q2.E
  N2: Q1.B, R9.Pin_1
  N3: Q1.C, 7_Segment1.common_anode
  N4: Q2.B, R10.Pin_1
  N5: Q2.C, 7_Segment2.common_anode
  N6: R2.Pin_1, Arduino1.D4
  N7: R3.Pin_1, Arduino1.D5
  N8: R4.Pin_1, Arduino1.D6
  N9: R5.Pin_1, Arduino1.D7
  N10: R6.Pin_1, Arduino1.D8
  N11: R7.Pin_1, Arduino1.D2
  N12: R8.Pin_1, Arduino1.D3
  N13: R9.Pin_0, Arduino1.D9
  N14: R10.Pin_0, Arduino1.D10
  N15: 7_Segment1.Segment_E, 7_Segment2.Segment_E
  N16: 7_Segment1.Segment_D, 7_Segment2.Segment_D
  N17: 7_Segment1.Segment_C, 7_Segment2.Segment_C
  N18: 7_Segment1.Segment_B, 7_Segment2.Segment_B
  N19: 7_Segment1.Segment_A, 7_Segment2.Segment_A
  N20: 7_Segment1.Segment_F, 7_Segment2.Segment_F
  N21: 7_Segment1.Segment_G, 7_Segment2.Segment_G
