# Fritzing sketch id1162_Texto_en_movimiento_LCD__con_potenciometro_0 (saved by Fritzing 0.9.2b)
breadboards: 1

parts:
  Parte1 = Arduino Uno (Rev3)
  LCD1 = LCD screen
  R2 = Rotary Potentiometer (Large) [maximum_resistance=100kΩ package=THT]

nets:
  N1: Parte1.D11_PWM/MOSI, LCD1.E
  N2: Parte1.D12/MISO, LCD1.RS
  N3: Parte1.D2, LCD1.DB7
  N4: Parte1.D3_PWM, LCD1.DB6
  N5: Parte1.D4, LCD1.DB5
  N6: Parte1.D5_PWM, LCD1.DB4
  5V: Parte1.5V, LCD1.VDD, LCD1.LED+, R2.leg2
  GND: Parte1.GND, LCD1.VSS, LCD1.R/W, LCD1.LED-, R2.leg1
  N7: LCD1.V0, R2.wiper
