# Fritzing sketch id1163_Control_PWM_Motor_CD_0 (saved by Fritzing 0.9.3b)
breadboards: 1

parts:
  M1 = DC Motor
  Q1 = NPN-Transistor [package="TO92 [THT]"]
  R1 = Resistor [tolerance=±5% resistance=10k package=THT]
  R2 = Rotary Potentiometer (Small) [maximum_resistance=100kΩ package=THT]
  Componente1 = Arduino Uno (Rev3)
  D1 = Rectifier Diode [part_number=1N4001 package="300 mil [THT]"]  # not connected

nets:
  N1: M1.pin_1, Q1.C
  N2: M1.pin_2, R1.Pin_0, R2.leg2, Componente1.5V
  N3: Q1.E, R2.leg1, Componente1.GND
  N4: Q1.B, R1.Pin_1, Componente1.D9_PWM
