# Fritzing sketch id1164_Control_servo_con_LCD_0 (saved by Fritzing 0.9.1b)
breadboards: 1

parts:
  LCD1 = LCD screen
  R1 = Rotary Potentiometer (Small) [maximum_resistance=100kΩ package=THT]
  R2 = Rotary Potentiometer (Small) [maximum_resistance=100kΩ package=THT]
  Parte1 = Arduino Mega ADK (Rev3)
  J1 = Basic Servo

nets:
  VSS: LCD1.VSS, LCD1.R/W, LCD1.LED-, R1.leg1, R2.leg2, Parte1.GND
  VDD: LCD1.VDD, LCD1.LED+, R1.leg2, R2.leg1, Parte1.5V
  N1: LCD1.V0, R2.wiper
  N2: LCD1.RS, Parte1.D12_PWM
  N3: LCD1.E, Parte1.D11_PWM
  N4: LCD1.DB4, Parte1.D5_PWM
  N5: LCD1.DB5, Parte1.D4_PWM
  N6: LCD1.DB6, Parte1.D3_PWM
  N7: LCD1.DB7, Parte1.D2_PWM
  N8: R1.wiper, Parte1.A0
  N9: Parte1.D9_PWM, J1.pulse

notes:
  Potenciometro de control del servo
  Potenciómetro de control del contraste del LCD
  //Código para Arduino
  //----------------------------------
  //Control de servo con LCD
  //----------------------------------
  //2014 - Sebastián de los Angeles
  //Este código se basa en los siguientes tutoriales disponibles en
  //la página oficial de Arduino ( http://arduino.cc ):
  // Knob: http://arduino.cc/en/Tutorial/Knob de Michal Rinott ( http://people.interaction-ivrea.it/m.rinott )
  // LiquidCrystal - "Hello World!": http://arduino.cc/en/Tutorial/LiquidCrystal de Tom Igoe
  //
  #include <Servo.h>
  #include <LiquidCrystal.h>
  LiquidCrystal lcd(12, 11, 5, 4, 3, 2); //Conexiones del LCD
  Servo miServo; //Creación del objeto Servo para acceder al mismo
  int pot_pin = 0; // Pin del potenciómetro
  int servo_pin = 9; // Pin de control del servo
  int val; // Variable donde almacenaremos el valor del potenciómetro
  int val2; // Variable auxiliar para cálculos con el valor del potenciómetro
  void setup()
  {
  lcd.begin(16, 2); //Activación del LCD
  miServo.attach(servo_pin); // Activación del servo en el pin designado
  }
  void loop()
  {
  lcd.setCursor(0,0); //Posicionamiento del cursor en el primer renglón, primera posición del LCD
  lcd.print("Posicion"); //Escribimos "Posición" en el LCD
  val = analogRead(pot_pin); // Lee el valor del potenciómetro (un valor entre 0 y 1023)
  val2 = map(val, 0, 1023, 0, 179); // Escalado del valor del potenciómetro para usarlo con el servo (un valor entre 0 y 180)
  miServo.write(val2); // Aplica el valor calculado al servo
  delay(15); // Demora para esperar a que el servo aplique los cambios indicados
  if(val2<100){// Mejora la visualización de los valores en la pantalla, poniendo un 0 delante de los valores menores que 100
  lcd.setCursor(0,1); //Posicionamiento del cursor en el segundo renglón, primera posición del LCD
  lcd.write("0"); //Escribimos el "0" delante
  lcd.setCursor(1,1);
  lcd.print(val2); // Escribimos el valor que le pasamos al servo en pantalla.
  }
  else{
  lcd.setCursor(0,1); //Posicionamiento del cursor en el segundo renglón, primera posición del LCD
  lcd.print(val2); // Escribimos el valor que le pasamos al servo en pantalla.
  }
  }
