# Fritzing sketch id1165_doors2_0 (saved by Fritzing 0.9.2b)
breadboards: 1

parts:
  S1 = Reed switch [package=THT]
  Part1 = Spark Core (v1.0)
  LED1 = LEDs [package=led10mm]
  R1 = Resistor [tolerance=±5% resistance=220 package=THT]
  R2 = Resistor [tolerance=±5% resistance=220 package=THT]

nets:
  N1: S1.pin_2, Part1.GND, LED1.C
  N2: Part1.A7, R2.Pin_0
  N3: Part1.D0, R1.Pin_0
  N4: LED1.A, R1.Pin_1
