# Fritzing sketch id1166_Placa_compatibilidad_PICAXE (saved by Fritzing 0.6.3b)
breadboards: 1

parts:
  U1 = Voltage Regulator - 5V [package="TO220 [THT]"]
  C1 = Electrolytic Capacitor [capacitance=1µF package="100 mil [THT, electrolytic]"]
  TRS1 = Stereo Jack (TRS) 3.5mm [package="PG203J [THT]"]
  J2 = female pin header, 3 pins [form="♀ (female)"]
  IC1 = IC, DIP package, 8 pins [chip_label=IC spacing=300mil]
  R1 = Resistor [tolerance=±5% resistance=10k package=THT]
  R2 = Resistor [tolerance=±5% resistance=22k package=THT]
  IC2 = IC, DIP package, 8 pins [chip_label=IC spacing=300mil]
  IC3 = IC, DIP package, 20 pins [chip_label=IC spacing=300mil]
  J3 = female pin header, 10 pins [form="♀ (female)"]
  J4 = female pin header, 10 pins [form="♀ (female)"]
  R3 = Resistor [tolerance=±5% resistance=4.7k package=THT]
  S1 = Pushbutton [package="[THT]"]
  J1 = Screw terminal - 2 pins [package=THT]
  R4 = Resistor [tolerance=±5% resistance=220 package=THT]
  LED1 = LED - 5mm [color="Red (633nm)" package="5 mm [THT]"]
  C2 = Electrolytic Capacitor [capacitance=1µF package="100 mil [THT, electrolytic]"]

nets:
  N1: U1.input_voltage, C1.+, J1.pin2
  N2: U1.GND, C1.-, IC1.pin4, R1.Pin_0, IC2.pin4, J1.pin1, R4.Pin_1, C2.-
  N3: U1.output_voltage, TRS1.Tip, J2.pin1, IC1.pin3, IC2.pin3, LED1.anode, C2.+
  N4: TRS1.Sleeve, J2.pin2, IC1.pin2, IC2.pin2
  N5: TRS1.Ring, J2.pin3, R1.Pin_1, R2.Pin_1
  N6: IC1.pin1, R2.Pin_0, IC2.pin1
  N7: IC1.pin5, IC3.pin8, IC3.pin20, J3.pin1, J4.pin8
  N8: IC1.pin6, IC3.pin1, J4.pin1
  N9: IC1.pin7, IC3.pin7, IC3.pin19, J3.pin2, J4.pin7
  N10: IC1.pin8, IC2.pin7, IC3.pin2, J4.pin2
  N11: IC2.pin5, IC3.pin5, IC3.pin17, J3.pin4, J4.pin5
  N12: IC2.pin6, IC3.pin16, J3.pin5, R3.Pin_1
  N13: IC2.pin8, IC3.pin3, J4.pin3
  N14: IC3.pin4, J4.pin4, R3.Pin_0, S1.Pin_1, S1.Pin_2
  N15: IC3.pin6, IC3.pin18, J3.pin3, J4.pin6
  N16: IC3.pin9, J4.pin9
  N17: IC3.pin10, J4.pin10
  N18: IC3.pin11, J3.pin10
  N19: IC3.pin12, J3.pin9
  N20: IC3.pin13, J3.pin8
  N21: IC3.pin14, J3.pin7
  N22: IC3.pin15, J3.pin6
  N23: S1.Pin_3, S1.Pin_4
  N24: R4.Pin_0, LED1.cathode
