# Fritzing sketch id1166_semaforo_0 (saved by Fritzing 0.9.2b)
breadboards: 1

parts:
  Parte1 = Arduino Uno (Rev3)  # not connected
  R1 = Resistor [tolerance=±5% resistance=220 package=THT]
  R2 = Resistor [tolerance=±5% resistance=220 package=THT]
  R3 = Resistor [tolerance=±5% resistance=220 package=THT]
  LED2 = smd LED [color="Red (633nm)" package="0603 [SMD]"]
  LED3 = smd LED [color="Yellow (595nm)" package="0603 [SMD]"]
  LED4 = smd LED [color="Green (570nm)" package="0603 [SMD]"]

nets:
  N1: R1.Pin_0, LED4.cathode
  N2: R1.Pin_1, R2.Pin_1, R3.Pin_1
  N3: R2.Pin_0, LED3.cathode
  N4: R3.Pin_0, LED2.cathode
