# Fritzing sketch id1168_Control_Electric_Door_Strike_0 (saved by Fritzing 0.9.2b)
breadboards: 1

parts:
  부품1 = Arduino Uno (Rev3)
  S1 = Pushbutton [package="[THT]"]
  KY-3 = keyes
  R1 = Resistor [tolerance=±5% resistance=10k package=THT]

nets:
  N1: 부품1.D8, KY-3.connector2
  N2: 부품1.D9_PWM, S1.Pin_3, S1.Pin_4, R1.Pin_1
  N3: 부품1.5V, S1.Pin_1, S1.Pin_2, KY-3.connector0
  N4: 부품1.GND, KY-3.connector1, R1.Pin_0

notes:
  Electric Door stirike
  12V VCC
  12V GND
