# Fritzing sketch id1169_Control_Electric_Door_Strike_By_BLUNO_0 (saved by Fritzing 0.9.2b)

parts:
  부품1 = Arduino Uno (Rev3)
  KY-3 = keyes

nets:
  N1: 부품1.D8, KY-3.connector2
  N2: 부품1.5V, KY-3.connector0
  N3: 부품1.GND, KY-3.connector1

notes:
  Electric Door stirike
  12V VCC
  12V GND
