# Fritzing sketch id116_circuit_4_2_0 (saved by Fritzing 0.9.1b)
breadboards: 1

parts:
  부품1 = Arduino Uno (Rev3)
  S1 = Pushbutton [package="[THT]"]

nets:
  N1: 부품1.D13/SCK, S1.Pin_3, S1.Pin_4
  N2: 부품1.5V, S1.Pin_1, S1.Pin_2
