# Fritzing sketch id1170_Stepper_Motor_0 (saved by Fritzing 0.9.2b)
breadboards: 1

parts:
  부품1 = Arduino Uno (Rev3)
  C1 = Electrolytic Capacitor [capacitance=100µF package="100 mil [THT, electrolytic]"]
  MD09B2 = A4988 Stepper Motor Driver Carrier
  M1 = Stepper Motor - Bipolar

nets:
  N1: 부품1.D4, MD09B2.DIR
  N2: 부품1.D5_PWM, MD09B2.STEP
  N3: 부품1.D6_PWM, MD09B2.Enable
  5V: 부품1.5V, MD09B2.MS2, MD09B2.VDD
  N4: 부품1.GND, MD09B2.MS1, MD09B2.MS3, MD09B2.GROUND#147
  N5: C1.-, MD09B2.GROUND#141
  N6: C1.+, MD09B2.VMOT
  N7: MD09B2.RESET, MD09B2.SLEEP
  N8: MD09B2.OUT_2B, M1.A
  N9: MD09B2.OUT_2A, M1.C
  N10: MD09B2.OUT_1A, M1.B
  N11: MD09B2.OUT_1B, M1.D
