# Fritzing sketch id1171_Control_LED_brightness_by_potentiometer_0 (saved by Fritzing 0.9.3b)
circuit board: 12.084cm x 6.70914cm
breadboards: 1

parts:
  Mega2560 = Arduino Mega 2560 (Rev3)
  R1 = Trimmer Potentiometer [maximum_resistance=50kΩ package=THT]
  LED1 = LED - 5mm [color="Red (633nm)" package="5 mm [THT]"]
  R2 = Resistor [tolerance=±5% resistance=220 package=THT]

nets:
  N1: Mega2560.A0, R1.wiper
  N2: Mega2560.5V, R1.leg1, LED1.cathode
  N3: Mega2560.GND, R1.leg2
  N4: Mega2560.D44, R2.Pin_1
  N5: LED1.anode, R2.Pin_0
