# Fritzing sketch id1173_Control_LEDs_with_DIP_switch_0 (saved by Fritzing 0.8.3b)
breadboards: 1

parts:
  Part1 = LilyPad Coin Cell Battery Holder
  SW3 = DIP SWITCH [package=dipswitch-02]
  SW4 = DIP SWITCH [package=dipswitch-02]
  LED1 = LED - 5mm [color="Red (633nm)" package="5 mm [THT]"]
  LED2 = LED - 5mm [color="Yellow (595nm)" package="5 mm [THT]"]
  LED3 = LED - 5mm [color="Green (570nm)" package="5 mm [THT]"]
  LED4 = LED - 5mm [color="Blue (470nm)" package="5 mm [THT]"]
  R1 = Resistor [tolerance=±5% resistance=470 package=THT]
  R2 = Resistor [tolerance=±5% resistance=470 package=THT]
  R3 = Resistor [tolerance=±5% resistance=470 package=THT]
  R4 = Resistor [tolerance=±5% resistance=470 package=THT]
  U1 = SWITCH_SPDT [package=kps-1290]

nets:
  N1: Part1.-, LED1.anode, LED2.anode, LED3.anode, LED4.anode
  N2: Part1.+, U1.O
  N3: SW3.1, LED1.cathode, R1.Pin_0, R1.Pin_1
  N4: SW3.2, LED2.cathode, R2.Pin_0, R2.Pin_1
  N5: SW3.3, SW3.4, SW4.3, SW4.4, U1.P
  N6: SW4.1, LED4.cathode, R3.Pin_0, R3.Pin_1
  N7: SW4.2, LED3.cathode, R4.Pin_0, R4.Pin_1
