# Fritzing sketch id1174_Control_light_switch_by_arduino_0 (saved by Fritzing 0.9.2b)
breadboards: 1

parts:
  부품1 = Arduino Uno (Rev3)
  부품2 = HC-06
  J1 = Basic Servo

nets:
  N1: 부품1.D9_PWM, J1.pulse
  N2: 부품1.D10_PWM/SS, 부품2.connector13
  N3: 부품1.D11_PWM/MOSI, 부품2.connector12
  5V: 부품1.5V, 부품2.connector15, J1.vcc
  GND: 부품1.GND, 부품2.connector14, J1.gnd
