# Fritzing sketch id1175_control_light_with_remote_controller_0 (saved by Fritzing 0.9.3b)

parts:
  Part1 = Arduino Uno (Rev3)
  LED1 = LED - 5mm [color="Red (633nm)" package="5 mm [THT]"]
  IR1 = TSOP312.., 314.. [package=THT]

nets:
  N1: Part1.D10_PWM/SS, LED1.anode
  N2: Part1.GND, LED1.cathode, IR1.Vs
  N3: Part1.D3_PWM, IR1.GND
  N4: Part1.5V, IR1.Data
