# Fritzing sketch id1176_motor_0 (saved by Fritzing 0.9.2b)
circuit board: 7.18747cm x 5.81596cm
breadboards: 1

parts:
  K1 = Relay [part_number=FRS1B-S package=THT]
  K2 = Relay [part_number=FRS1B-S package=THT]
  M1 = DC Motor
  D1 = Rectifier Diode [part_number=1N4001 package="300 mil [THT]"]
  D2 = Rectifier Diode [part_number=1N4001 package="300 mil [THT]"]
  Q1 = NPN-Transistor [package="TO92 [THT]"]
  Q2 = NPN-Transistor [package="TO92 [THT]"]
  R1 = Resistor [tolerance=±5% resistance=2.2k package=THT]
  R2 = Resistor [tolerance=±5% resistance=2.2k package=THT]
  12_V = Power plug
  24_V = Power plug
  Componente1 = Arduino Uno (Rev3)
  Start = Pushbutton [package=THT]
  Stop = Pushbutton [package=THT]

nets:
  GND: K1.A, K2.A, Q1.E, Q2.E, 12_V.GND, 24_V.GND, Componente1.GND, Start.leg1, Stop.leg1
  N1: K1.COIL1, D1.anode, Q1.C
  N2: K1.C1, K1.C2, M1.pin_1
  N3: K1.COIL2, K2.COIL2, D1.cathode, D2.cathode, 12_V.VCC
  N4: K1.B, K2.B, 24_V.VCC
  N5: K2.COIL1, D2.anode, Q2.C
  N6: K2.C1, K2.C2, M1.pin_2
  N7: Q1.B, R1.Pin_1
  N8: Q2.B, R2.Pin_0
  N9: R1.Pin_0, Componente1.D3_PWM
  N10: R2.Pin_1, Componente1.D2
  N11: Componente1.D0/RX, Start.leg0
  N12: Componente1.D1/TX, Stop.leg0
  5V: Componente1.5V

notes:
  12 V coil (relay)
  24 V motor
