# Fritzing sketch id1177_Pet_Feeder_0 (saved by Fritzing 0.9.2b)
breadboards: 1

parts:
  부품1 = Arduino Uno (Rev3)
  D1 = Rectifier Diode [part_number=1N4004 package="300 mil [THT]"]
  KY-1 = keyes
  M1 = DC Motor
  S1 = Momentary Switch [package=ksa_sealed_tac_switch]
  R1 = Resistor [tolerance=±5% resistance=10k package=THT]

nets:
  N1: 부품1.GND, KY-1.connector2, M1.pin_2, R1.Pin_0
  N2: 부품1.D2, KY-1.connector0
  N3: 부품1.D3_PWM, S1.3, R1.Pin_1
  N4: 부품1.5V, KY-1.connector1, S1.1
  N5: 부품1.VIN, D1.anode
  N6: D1.cathode, KY-1.connector5
  N7: KY-1.connector4, M1.pin_1
