# Fritzing sketch id1179_trackball_rgbstrip_0 (saved by Fritzing 0.8.3b)
circuit board: 7.05552cm x 5.588cm
breadboards: 1

parts:
  Composants1 = Arduino Uno (Rev3)
  RGB_LED_STRIP = RGB LED (com. anode, rbg) [package="5 mm [THT]"]
  R1 = Resistor [tolerance=±5% resistance=1k package=THT]
  Q1 = NPN-Transistor [part_number=2N2222 package="TO92 [THT]"]
  Q2 = NPN-Transistor [part_number=2N2222 package="TO92 [THT]"]
  Q3 = NPN-Transistor [part_number=2N2222 package="TO92 [THT]"]
  R2 = Resistor [tolerance=±5% resistance=1k package=THT]
  R3 = Resistor [tolerance=±5% resistance=1k package=THT]
  Power_plug_-_12V = Power plug
  Trackball = mystery part, 4 pins [chip_label=trackball]

nets:
  GND: Composants1.GND, Q1.C, Q2.C, Q3.C, Power_plug_-_12V.GND, Trackball.pin1
  N1: Composants1.D9_PWM, R1.Pin_1
  N2: Composants1.D10_PWM/SS, R2.Pin_1
  N3: Composants1.D11_PWM/MOSI, R3.Pin_1
  N4: Composants1.D5_PWM, Trackball.pin4
  N5: Composants1.D6_PWM, Trackball.pin3
  N6: Composants1.5V, Trackball.pin2
  VIN: Composants1.VIN, RGB_LED_STRIP.common_anode, Power_plug_-_12V.VCC
  N7: RGB_LED_STRIP.red_cathode, Q3.E
  N8: RGB_LED_STRIP.blue_cathode, Q2.E
  N9: RGB_LED_STRIP.green_cathode, Q1.E
  N10: R1.Pin_0, Q1.B
  N11: Q2.B, R2.Pin_0
  N12: Q3.B, R3.Pin_0

notes:
  trackbal pinout
  GND
  + 5V
  CLOCK
  DATA
  RGB Led Strip
