# Fritzing sketch id117_4Btn_0 (saved by Fritzing 0.9.1b)
circuit board: 14.1173cm x 7.76041cm

parts:
  Part1 = Arduino Uno (Rev3)
  S1 = SWITCH-MOMENTARY-2 [package=tactile-pth-12mm]
  S2 = SWITCH-MOMENTARY-2 [package=tactile-pth-12mm]
  S3 = SWITCH-MOMENTARY-2 [package=tactile-pth-12mm]
  S4 = SWITCH-MOMENTARY-2 [package=tactile-pth-12mm]
  D1 = Zener Diode [part_number=1N4732A breakdown_voltage=3.6V package="300 mil [THT]"]
  D2 = Zener Diode [part_number=1N4732A breakdown_voltage=3.6V package="300 mil [THT]"]
  R1 = Resistor [tolerance=±5% resistance=10k package=THT]
  R2 = Resistor [tolerance=±5% resistance=10k package=THT]

nets:
  N1: Part1.D2, S3.1, S4.1
  N2: Part1.D3_PWM, S1.1, S2.1
  N3: Part1.D4, S2.2, D2.cathode, R2.Pin_1
  N4: Part1.D5_PWM, S1.2, D1.cathode, R1.Pin_1
  N5: Part1.GND, R1.Pin_0, R2.Pin_0
  N6: S3.2, D1.anode
  N7: S4.2, D2.anode
