# Fritzing sketch id1180_proto_rgb_with_switches_0 (saved by Fritzing 0.7.12b)
breadboards: 2

parts:
  LED1 = RGB LED (com. anode, rbg) [package="5 mm [THT]"]
  Arduino1 = Arduino
  TLC5940NT1 = TLC5940NT
  TLC5940NT2 = TLC5940NT
  TLC5940NT3 = TLC5940NT
  LED2 = RGB LED (com. anode, rbg) [package="5 mm [THT]"]
  R1 = Resistor [tolerance=±5% resistance=2.2k package=THT]
  R2 = Resistor [tolerance=±5% resistance=2.2k package=THT]
  R3 = Resistor [tolerance=±5% resistance=2.2k package=THT]
  LED3 = RGB LED (com. anode, rbg) [package="5 mm [THT]"]
  S1 = Pushbutton [package="[THT]"]
  R4 = Resistor [tolerance=±5% resistance=10k package=THT]

nets:
  N1: LED1.common_anode, Arduino1.+5V, TLC5940NT1.connector18, TLC5940NT1.connector20, TLC5940NT2.connector18, TLC5940NT2.connector20, TLC5940NT3.connector18, TLC5940NT3.connector20, LED2.common_anode, LED3.common_anode, S1.Pin_1, S1.Pin_2
  N2: LED1.blue_cathode, TLC5940NT2.connector27
  N3: LED1.green_cathode, TLC5940NT3.connector27
  N4: Arduino1.D6, S1.Pin_3, S1.Pin_4, R4.Pin_1
  N5: Arduino1.GND, TLC5940NT1.connector21, TLC5940NT1.connector26, TLC5940NT2.connector21, TLC5940NT3.connector21, TLC5940NT3.connector26, R1.Pin_1, R2.Pin_1, R3.Pin_1
  N6: TLC5940NT1.connector0, LED2.red_cathode
  N7: TLC5940NT1.connector1, LED3.red_cathode
  N8: TLC5940NT1.connector16, TLC5940NT2.connector25
  N9: TLC5940NT1.connector19, R1.Pin_0
  N10: TLC5940NT1.connector24, TLC5940NT2.connector24, TLC5940NT3.connector24
  N11: TLC5940NT2.connector0, LED2.blue_cathode
  N12: TLC5940NT2.connector1, LED3.blue_cathode
  N13: TLC5940NT2.connector16, TLC5940NT3.connector25
  N14: TLC5940NT2.connector19, R2.Pin_0
  N15: TLC5940NT3.connector0, LED2.green_cathode
  N16: TLC5940NT3.connector1, LED3.green_cathode
  N17: TLC5940NT3.connector19, R3.Pin_0

notes:
  My 10mm RGB's are R, Anode, G, B.
  So the 1st TLC on the left controls red, the middle green and the right TLC the blue pins
