# Fritzing sketch id1182_servo_serial_fritzing_0 (saved by Fritzing 0.9.3b)

parts:
  J1 = Basic Servo
  부품1 = Arduino Uno (Rev3)

nets:
  GND: J1.gnd, 부품1.GND
  VCC: J1.vcc, 부품1.5V
  N1: J1.pulse, 부품1.D9_PWM
