# Fritzing sketch id1183_MeArm_0 (saved by Fritzing 0.9.2b)
breadboards: 1

parts:
  Part1 = Arduino Uno (Rev3)
  J1 = Basic Servo
  J2 = Basic Servo
  J3 = Basic Servo
  J4 = Basic Servo
  R1 = Trimmer Potentiometer [maximum_resistance=10kΩ package=THT]
  R2 = Trimmer Potentiometer [maximum_resistance=10kΩ package=THT]
  R3 = Trimmer Potentiometer [maximum_resistance=10kΩ package=THT]
  R4 = Trimmer Potentiometer [maximum_resistance=10kΩ package=THT]

nets:
  N1: Part1.A0, R3.wiper
  N2: Part1.A1, R2.wiper
  N3: Part1.A2, R4.wiper
  N4: Part1.A3, R1.wiper
  N5: Part1.D9_PWM, J4.pulse
  N6: Part1.D10_PWM/SS, J1.pulse
  N7: Part1.D11_PWM/MOSI, J2.pulse
  N8: Part1.D12/MISO, J3.pulse
  VCC: Part1.5V, J1.vcc, J2.vcc, J3.vcc, J4.vcc, R1.leg2, R2.leg2, R3.leg2, R4.leg2
  N9: J1.gnd, R2.leg1
  N10: J2.gnd, R4.leg1
  N11: J3.gnd, R1.leg1
  N12: J4.gnd, R3.leg1
