# Fritzing sketch id1185_reed_switch_0 (saved by Fritzing 0.9.2b)
breadboards: 1

parts:
  부품1 = Arduino Uno (Rev3)
  S1 = Reed switch [package=THT]
  LED1 = LED - 5mm [color="Red (633nm)" package="5 mm [THT]"]
  R1 = Resistor [tolerance=±5% resistance=220 package=THT]
  R2 = Resistor [tolerance=±5% resistance=10k package=THT]

nets:
  N1: 부품1.D13/SCK, R1.Pin_1
  N2: 부품1.D2, S1.pin_2, R2.Pin_0
  N3: 부품1.5V, S1.pin_1
  N4: 부품1.GND, LED1.cathode, R2.Pin_1
  N5: LED1.anode, R1.Pin_0
