# Fritzing sketch id1186_ble_0 (saved by Fritzing 0.9.2b)
circuit board: 8.46667cm x 5.64444cm
breadboards: 1

parts:
  Part1 = adafruit [part_number="Adafruit #2479"]
  Part2 = Arduino Pro Mini v13
  LED1 = LED - 5mm [color="Red (633nm)" package="5 mm [THT]"]
  R1 = Resistor [tolerance=±5% resistance=220 package=THT]
  J1 = Piezo Speaker

nets:
  N1: Part1.connector27, Part2.GND, Part2.D6_PWM, LED1.cathode, J1.pin1, J1.pin2
  N2: Part1.connector29, Part2.VCC
  N3: Part1.connector30, Part2.D9_PWM
  N4: Part1.connector31, Part2.D10_PWM/SS
  N5: Part1.connector32, Part2.D11_PWM/MOSI
  N6: Part1.connector33, Part2.D12/MISO
  N7: Part2.D3_PWM, R1.Pin_0
  N8: LED1.anode, R1.Pin_1

notes:
  https://anasdalintakam.blogspot.in/
