# Fritzing sketch id1187_arduino_8_leds_ci_74hc595_0 (saved by Fritzing 0.7.12b)
breadboards: 1

parts:
  U1 = 74HC595 [package="DIP16 [THT]"]
  LED1 = LED - 5mm [color="Blue (430nm)" package="5 mm [THT]"]
  LED2 = LED - 5mm [color="Blue (430nm)" package="5 mm [THT]"]
  LED3 = LED - 5mm [color="Blue (430nm)" package="5 mm [THT]"]
  LED4 = LED - 5mm [color="Blue (430nm)" package="5 mm [THT]"]
  LED5 = LED - 5mm [color="Blue (430nm)" package="5 mm [THT]"]
  LED6 = LED - 5mm [color="Blue (430nm)" package="5 mm [THT]"]
  LED7 = LED - 5mm [color="Blue (430nm)" package="5 mm [THT]"]
  LED8 = LED - 5mm [color="Blue (430nm)" package="5 mm [THT]"]
  Arduino1 = Arduino
  R1 = Resistor [tolerance=±5% resistance=330 package=THT]
  R2 = Resistor [tolerance=±5% resistance=330 package=THT]
  R3 = Resistor [tolerance=±5% resistance=330 package=THT]
  R4 = Resistor [tolerance=±5% resistance=330 package=THT]
  R5 = Resistor [tolerance=±5% resistance=330 package=THT]
  R6 = Resistor [tolerance=±5% resistance=330 package=THT]
  R7 = Resistor [tolerance=±5% resistance=330 package=THT]
  R8 = Resistor [tolerance=±5% resistance=330 package=THT]

nets:
  N1: U1.Q1, LED2.anode, R7.Pin_0, R7.Pin_1
  N2: U1.Q2, LED4.anode, R6.Pin_0, R6.Pin_1
  N3: U1.Q3, LED3.anode, R5.Pin_0, R5.Pin_1
  N4: U1.Q4, LED5.anode, R4.Pin_0, R4.Pin_1
  N5: U1.Q5, LED6.anode, R3.Pin_0, R3.Pin_1
  N6: U1.Q6, LED7.anode, R2.Pin_0, R2.Pin_1
  N7: U1.Q7, LED8.anode, R1.Pin_0, R1.Pin_1
  GND: U1.GND, U1.OE, LED1.cathode, LED2.cathode, LED3.cathode, LED4.cathode, LED5.cathode, LED6.cathode, LED7.cathode, LED8.cathode, Arduino1.GND
  VCC: U1.MR, U1.VCC, Arduino1.+5V
  N8: U1.SH_CP, Arduino1.D2
  N9: U1.ST_CP, Arduino1.D3
  N10: U1.DS, Arduino1.D4
  N11: U1.Q0, LED1.anode, R8.Pin_0, R8.Pin_1
