# Fritzing sketch id1188_arduino_motor_cc_0 (saved by Fritzing 0.7.10b)
breadboards: 1

parts:
  R1 = Rotary Potentiometer (Large) [maximum_resistance=10kΩ package=THT]
  Arduino1 = Arduino
  D1 = Rectifier Diode [part_number=1N4001 package="300 mil [THT]"]
  VCC1 = 4 x AAA Battery Mount
  Q1 = NPN-Transistor [package="TO92 [THT]"]
  M1 = DC Motor

nets:
  N1: R1.leg1, Arduino1.GND, D1.anode, VCC1.-, Q1.C
  N2: R1.wiper, Arduino1.A0
  N3: R1.leg2, Arduino1.+5V
  N4: Arduino1.D9, Q1.E
  N5: D1.cathode, Q1.B, M1.pin_2
  N6: VCC1.+, M1.pin_1
