# Fritzing sketch id1190_Projeto_Arduino_controlando_led_RGB_multicolorido_0 (saved by Fritzing 0.7.12b)
breadboards: 1

parts:
  Arduino1 = Arduino
  R1 = Resistor [tolerance=±5% resistance=330 package=THT]
  R2 = Resistor [tolerance=±5% resistance=330 package=THT]
  R3 = Resistor [tolerance=±5% resistance=330 package=THT]
  LED1 = RGB LED - (4 legs) [package="5 mm [THT]"]

nets:
  N1: Arduino1.D10, R2.Pin_0, R2.Pin_1, LED1.red_cathode
  N2: Arduino1.D9, R3.Pin_0, R3.Pin_1, LED1.green_cathode
  N3: Arduino1.D8, R1.Pin_0, R1.Pin_1, LED1.blue_cathode
  N4: Arduino1.GND, LED1.common_anode
