# Fritzing sketch id1191_pontenciometroMotorMcArduino_0 (saved by Fritzing 0.9.2b)
breadboards: 1

parts:
  Parte1 = Arduino Uno (Rev3)
  VCC1 = Battery
  M1 = DC Motor
  Q1 = NPN-Transistor [package="TO92 [THT]"]
  R1 = Resistor [tolerance=±5% resistance=220 package=THT]
  R2 = Rotary Potentiometer (Small) [maximum_resistance=100kΩ package=THT]

nets:
  N1: Parte1.A0, R2.wiper
  N2: Parte1.D3_PWM, R1.Pin_1
  N3: Parte1.5V, VCC1.+, M1.pin_2, R2.leg1
  N4: Parte1.GND, VCC1.-, Q1.C, R2.leg2
  N5: M1.pin_1, Q1.B
  N6: Q1.E, R1.Pin_0

notes:
  //Códigopara el Arduino
  int motoDC=5;
  void setup(){
  Serial.begin(9600);
  }
  void loop(){
  float niv=analogRead(A1)/4;
  analogWrite(motoDC, niv);
  Serial.println (niv);
  delay(1000);
  }
