# Fritzing sketch id1192_Controle_Acces_RFID_RC522_0 (saved by Fritzing 0.9.3b)

parts:
  VIN_12V = Arduino Uno (Rev3)
  Lecteur_RFID_RC522 = RFID-RC522
  3_3_V = RGB LED - (4 legs) [package="5 mm [THT]"]
  R1 = Resistor [tolerance=±5% resistance=2.2k package="2010 [SMD]"]
  RAZ_DataBase = Momentary Switch [package=ksa_sealed_tac_switch]
  Emet_un_son_quand_le_Badge_est_présenté = Piezo Speaker
  Pin_4_/_Sortie_/_GND = Basic FET N-Channel [package="TO220 [THT]"]
  OU1 = LCD screen
  Adr_0x3F = generic_ic_dip_22_300mil.fzp [part_number="LCM1602 I2c" chip_label="LCM1602 I2c"]
  JACK1 = 2.1mm_Barrel_Jack_with_Terminal_Block  # not connected

nets:
  N1: VIN_12V.A4/SDA, Adr_0x3F.connector18
  N2: VIN_12V.A5/SCL, Adr_0x3F.connector19
  N3: VIN_12V.D8, Emet_un_son_quand_le_Badge_est_présenté.pin2
  N4: VIN_12V.D9_PWM, Lecteur_RFID_RC522.connector14
  N5: VIN_12V.D10_PWM/SS, Lecteur_RFID_RC522.connector8
  N6: VIN_12V.D11_PWM/MOSI, Lecteur_RFID_RC522.connector10
  N7: VIN_12V.D12/MISO, Lecteur_RFID_RC522.connector11
  N8: VIN_12V.D13/SCK, Lecteur_RFID_RC522.connector9
  N9: VIN_12V.GND, Emet_un_son_quand_le_Badge_est_présenté.pin1
  N10: VIN_12V.D3_PWM, RAZ_DataBase.4
  N11: VIN_12V.D4, Pin_4_/_Sortie_/_GND.gate
  N12: VIN_12V.D5_PWM, 3_3_V.blue_cathode
  N13: VIN_12V.D6_PWM, 3_3_V.green_cathode
  N14: VIN_12V.D7, 3_3_V.red_cathode
  N15: VIN_12V.3V3, Lecteur_RFID_RC522.connector15
  N16: VIN_12V.5V, Adr_0x3F.connector17
  N17: Lecteur_RFID_RC522.connector13, R1.Pin_1
  N18: OU1.VSS, Adr_0x3F.connector0
  N19: OU1.VDD, Adr_0x3F.connector1
  N20: OU1.V0, Adr_0x3F.connector2
  N21: OU1.RS, Adr_0x3F.connector3
  N22: OU1.R/W, Adr_0x3F.connector4
  N23: OU1.E, Adr_0x3F.connector5
  N24: OU1.DB0, Adr_0x3F.connector6
  N25: OU1.DB1, Adr_0x3F.connector7
  N26: OU1.DB2, Adr_0x3F.connector8
  N27: OU1.DB3, Adr_0x3F.connector9
  N28: OU1.DB4, Adr_0x3F.connector10
  N29: OU1.DB5, Adr_0x3F.connector11
  N30: OU1.DB6, Adr_0x3F.connector12
  N31: OU1.DB7, Adr_0x3F.connector13
  N32: OU1.LED+, Adr_0x3F.connector14
  N33: OU1.LED-, Adr_0x3F.connector15

notes:
  Contrôle d'Acces avec un Badge RFID
  Un maintient de BP RAZ DataBase pendant + de 5s et un appuie bref sur RESET de la carte permet d'effacer la Base de données des Badges
  BLEU Attente de Badge
  ROUGE Accés Refusé
  VERT Accés Autorisé
  MULTIPLE Mode Programmation
  ATTENTION
  Alimentation de la carte en 3,3V
  1 - VCC <> 3,3V
  2 - RST <> Pin 9
  3 - GND <> GND
  4 - IRQ
  5 - MISO <> Pin 12
  6 - MOSI <> Pin 11
  7 - SCK <> Pin 13
  8 - SDA <> Pin 10
  Mosfet IRF3205
  Entre Sortie et VIN 12V on peut mettre
  * un Relais 12V
  * une serrure electrique...
  Entrée 12V
  pour Serrure
  récupéré sur VIN
  #include <LiquidCrystal_I2C.h>
  LiquidCrystal_I2C lcd(0x3F,20,4); // Adresse I2c, 20 caractéres, 4 lignes
  // Branchement SDA sur A4 ou SDA et SCL sur A5 ou SCL
  void setup()
  {
  // initialise le lcd
  lcd.init();
  lcd.backlight();
  lcd.clear();
  lcd.setCursor(0,0); // Curseur en Position 0,0
  lcd.print("Hello world..."); // Affiche Hello world...
