# Fritzing sketch id1193_tcc_placa_geral_0 (saved by Fritzing 0.9.0b)
breadboards: 1

parts:
  Componente1 = Arduino Uno (Rev3)
  R1 = Photocell (LDR) [package=THT]
  DHT1 = DHT11_Temperature_and_Humitidy_Sensor
  LCD1 = LCD screen
  U1 = POT [package=pot_alpha_rv16af-20]
  R2 = Resistor [tolerance=±5% resistance=330 package=THT]
  J1 = screw terminal, 3 pins  # not connected
  J2 = screw terminal, 3 pins  # not connected
  J3 = screw terminal, 3 pins  # not connected
  J4 = screw terminal, 3 pins  # not connected
  J5 = screw terminal, 6 pins
  K1 = Relay [part_number=FRS1B-S package=THT]  # not connected
  K2 = Relay [part_number=FRS1B-S package=THT]  # not connected
  K3 = Relay [part_number=FRS1B-S package=THT]  # not connected
  K4 = Relay [part_number=FRS1B-S package=THT]  # not connected
  LED1 = LEDs [package=led-1206]  # not connected

nets:
  N1: Componente1.A0, R1.pin_1, R2.Pin_0
  N2: Componente1.A5/SCL, DHT1.connector2
  N3: Componente1.D8, J5.pin3
  N4: Componente1.D11_PWM/MOSI, LCD1.E
  N5: Componente1.D12/MISO, LCD1.RS
  N6: Componente1.D13/SCK, J5.pin2
  N7: Componente1.D2, LCD1.DB7
  N8: Componente1.D3_PWM, LCD1.DB6
  N9: Componente1.D4, LCD1.DB5
  N10: Componente1.D5_PWM, LCD1.DB4
  N11: Componente1.D7, J5.pin4
  5V: Componente1.5V, DHT1.connector1, LCD1.VDD, LCD1.LED+, U1.A, R2.Pin_1, J5.pin6
  GND: Componente1.GND, R1.pin_0, DHT1.connector4, LCD1.VSS, LCD1.R/W, LCD1.LED-, U1.E, J5.pin1
  N12: LCD1.V0, U1.S

notes:
  Vcc
  IN4
  IN3
  IN2
  IN1
  GND
  NC
  NO
  C
