# Fritzing sketch id1194_relay_ADK_0 (saved by Fritzing 0.7.7b)
breadboards: 2

parts:
  IC1 = ULN2803A [package=THT]
  Arduino1 = Arduino Mega
  RELAY1 = Componente_sem_nome
  RELAY2 = Componente_sem_nome
  RELAY3 = Componente_sem_nome
  RELAY4 = Componente_sem_nome
  Power_plug1 = Power plug
  RELAY5 = Componente_sem_nome
  RELAY6 = Componente_sem_nome
  RELAY7 = Componente_sem_nome
  RELAY8 = Componente_sem_nome
  J1 = Screw terminal - 2 pins [package=THT]
  J2 = Screw terminal - 2 pins [package=THT]
  J3 = Screw terminal - 2 pins [package=THT]
  J4 = Screw terminal - 2 pins [package=THT]
  J5 = Screw terminal - 2 pins [package=THT]
  J6 = Screw terminal - 2 pins [package=THT]
  J7 = Screw terminal - 2 pins [package=THT]
  J8 = Screw terminal - 2 pins [package=THT]
  C1 = Electrolytic Capacitor [capacitance=100µF voltage=50V package="300 mil [THT, electrolytic]"]  # not connected
  R1 = Resistor [tolerance=±5% resistance=220 package=THT]

nets:
  N1: IC1.Out_1, RELAY1.connector0
  N2: Arduino1.GND, RELAY1.connector1, RELAY2.connector1, RELAY3.connector1, RELAY4.connector1, RELAY5.connector1, RELAY6.connector1, RELAY7.connector1, RELAY8.connector1, J1.pin2, J2.pin2, J3.pin2, J4.pin2
  N3: RELAY1.connector4, J1.pin1
  N4: RELAY2.connector4, J2.pin1
  N5: RELAY3.connector4, J3.pin1
  N6: RELAY4.connector4, J4.pin1
  N7: Power_plug1.VCC, R1.Pin_0
  N8: RELAY5.connector4, J5.pin1
  N9: RELAY6.connector4, J6.pin1
  N10: RELAY7.connector4, J7.pin1
  N11: RELAY8.connector4, J8.pin1
  N12: J5.pin2, J6.pin2, J7.pin2, J8.pin2

notes:
  Controling 8 Relay Output
  with Android Custom Apps
  connected via USB Host.
  5V USB
  12V External Power
  220Ω resistor
  1000µF capasitor
  ULN2803A IC
  http://blog.ozzie.web.id/?p=997
