# Fritzing sketch id1195_Controller_dual_channel_rgb_light_0 (saved by Fritzing 0.8.3b)
circuit board: 7.04927cm x 5.43121cm
breadboards: 1

parts:
  Componente1 = Arduino Uno (Rev3)
  Q1 = Basic FET N-Channel [package="TO220 [THT]"]
  Q2 = Basic FET N-Channel [package="TO220 [THT]"]
  Q3 = Basic FET N-Channel [package="TO220 [THT]"]
  R1 = Resistor [tolerance=±5% resistance=10k package=THT]
  R2 = Resistor [tolerance=±5% resistance=10k package=THT]
  R3 = Resistor [tolerance=±5% resistance=10k package=THT]
  J1 = Screw terminal - 2 pins [package=THT]
  J2 = Screw terminal - 2 pins [package=THT]
  VCC1 = prefix0000

nets:
  N1: Componente1.GND, Q1.source, Q2.source, Q3.source, R1.Pin_1, R2.Pin_1, R3.Pin_1, VCC1.connector0
  N2: Componente1.D9_PWM, Q1.gate
  N3: Componente1.D10_PWM/SS, Q2.gate
  N4: Componente1.D11_PWM/MOSI, Q3.gate
  N5: Q1.drain, R1.Pin_0, J1.pin2
  N6: Q2.drain, R3.Pin_0, J1.pin1
  N7: Q3.drain, R2.Pin_0, J2.pin2
  N8: J2.pin1, VCC1.connector1
