# Fritzing sketch id1196_servos_and_joystick_0 (saved by Fritzing 0.9.2b)
breadboards: 1

parts:
  Part1 = Arduino Uno (Rev3)
  Part2 = Thumb Joystick
  J1 = Basic Servo
  J2 = Basic Servo

nets:
  N1: Part1.A0, Part2.HORZ
  N2: Part1.A1, Part2.VERT
  N3: Part1.D9_PWM, J1.pulse
  N4: Part1.D10_PWM/SS, J2.pulse
  VCC: Part1.5V, Part2.VCC, J1.vcc, J2.vcc
  GND: Part1.GND, Part2.GND, J1.gnd, J2.gnd
