# Fritzing sketch id1197_Untitled_Sketch_0 (saved by Fritzing 0.9.0b)
breadboards: 1

parts:
  VCC1 = Battery
  Part1 = Arduino Leonardo (Rev3b)
  S1 = Pushbutton [package="[THT]"]
  M1 = DC Motor
  Q1 = Basic FET P-Channel [package="TO220 [THT]"]
  D1 = Schottky Diode [part_number=1N5817 package="Melf DO-213 AB [SMD]"]

nets:
  N1: VCC1.-, Part1.GND, M1.pin_2, D1.anode
  N2: VCC1.+, Q1.source
  N3: Part1.5V, S1.Pin_3, S1.Pin_4
  N4: Part1.A1, S1.Pin_1, S1.Pin_2
  N5: Part1.D9_PWM/A9, Q1.gate
  N6: M1.pin_1, Q1.drain, D1.cathode
