# Fritzing sketch id1198_Controlling_Brushless_DC_Motor_with_Arduino_and_Toggle_Switch_0 (saved by Fritzing 0.8.7b)
breadboards: 1

parts:
  Part1 = Arduino Uno (Rev3)
  J1 = Basic Servo
  S1 = Toggle Switch [package=THT]
  LED1 = LED - 5mm [color="Red (633nm)" package="5 mm [THT]"]
  R1 = Resistor [tolerance=±5% resistance=220 package=THT]

nets:
  N1: Part1.D8, S1.L1
  N2: Part1.D9_PWM, J1.pulse
  N3: Part1.D13/SCK, R1.Pin_0
  GND: Part1.GND, J1.gnd, S1.COM, LED1.cathode
  N4: LED1.anode, R1.Pin_1
