# Fritzing sketch id1199_Fritzing_car_0 (saved by Fritzing 0.9.2b)
breadboards: 1

parts:
  Arduino = Arduino Uno (Rev3)
  U1 = L298 [package=multiwatt15]
  M1 = DC Motor
  M2 = DC Motor
  VCC1 = Battery block 9V
  U2 = POT [package=alps_pot]
  S1 = SWITCH-MOMENTARY-2 [package=tactile-pth-12mm]
  R3 = Resistor [tolerance=±5% resistance=10k package="0603 [SMD]"]

nets:
  N1: Arduino.D8, U1.IN4
  N2: Arduino.D9_PWM, U1.ENA
  N3: Arduino.D10_PWM/SS, U1.ENB
  GND: Arduino.GND, U1.GND, VCC1.-, U2.A, R3.Pin_0
  N4: Arduino.D2, S1.2, R3.Pin_1
  N5: Arduino.D5_PWM, U1.IN1
  N6: Arduino.D6_PWM, U1.IN2
  N7: Arduino.D7, U1.IN3
  N8: Arduino.5V, U1.CSA, U2.E, S1.1
  N9: U1.OUT3, M1.pin_1
  N10: U1.OUT4, M2.pin_2
  N11: U1.CSB, VCC1.+
  N12: M1.pin_2, M2.pin_1
