# Fritzing sketch id119_7_digital_segment_add_buzzer_short_v2_lv1_0 (saved by Fritzing 0.9.2b)
breadboards: 1

parts:
  Part2 = Arduino Uno (Rev3)
  U3 = 74HC595 [package="DIP16 [THT]"]
  7_Segment_4_Digit_Display3 = MyPart1 [part_number=HS420561K-32]
  R17 = Resistor [tolerance=±5% resistance=220 package=THT]
  R18 = Resistor [tolerance=±5% resistance=220 package=THT]
  R19 = Resistor [tolerance=±5% resistance=220 package=THT]
  R20 = Resistor [tolerance=±5% resistance=220 package=THT]

nets:
  N1: Part2.D8, U3.DS
  N2: Part2.D9_PWM, U3.ST_CP
  N3: Part2.D10_PWM/SS, U3.SH_CP
  N4: Part2.D2, R18.Pin_0
  N5: Part2.D3_PWM, R20.Pin_0
  N6: Part2.D4, R19.Pin_0
  N7: Part2.D5_PWM, R17.Pin_0
  5V: Part2.5V, U3.MR, U3.VCC
  GND: Part2.GND, U3.GND, U3.OE
  N8: U3.Q1, 7_Segment_4_Digit_Display3.connector7
  N9: U3.Q2, 7_Segment_4_Digit_Display3.connector4
  N10: U3.Q3, 7_Segment_4_Digit_Display3.connector2
  N11: U3.Q4, 7_Segment_4_Digit_Display3.connector1
  N12: U3.Q5, 7_Segment_4_Digit_Display3.connector10
  N13: U3.Q6, 7_Segment_4_Digit_Display3.connector5
  N14: U3.Q7, 7_Segment_4_Digit_Display3.connector3
  N15: U3.Q0, 7_Segment_4_Digit_Display3.connector11
  N16: 7_Segment_4_Digit_Display3.connector6, R18.Pin_1
  N17: 7_Segment_4_Digit_Display3.connector8, R20.Pin_1
  N18: 7_Segment_4_Digit_Display3.connector9, R19.Pin_1
  N19: 7_Segment_4_Digit_Display3.connector12, R17.Pin_1
