# Fritzing sketch id11_Untitled_Sketch_0 (saved by Fritzing 0.9.2b)
breadboards: 1

parts:
  Часть1 = Arduino Uno (Rev3)
  LCD1 = LCD screen
  R1 = Rotary Potentiometer (Small) [maximum_resistance=100kΩ package=THT]

nets:
  N1: Часть1.D4, LCD1.RS
  N2: Часть1.D5_PWM, LCD1.E
  N3: Часть1.D6_PWM, LCD1.DB4
  N4: Часть1.D7, LCD1.DB5
  5V: Часть1.5V, LCD1.VDD, R1.leg1
  GND: Часть1.GND, LCD1.VSS, LCD1.R/W, R1.leg2
  N5: LCD1.V0, R1.wiper
