# Fritzing sketch id1200_ControllinoMixerSdCardBoardLogo_0 (saved by Fritzing 0.9.2b)
circuit board: 16cm x 10cm
breadboards: 2

parts:
  Shield-Connector = Arduino Mega 2560 (Rev3)
  X1 = shrouded pin header, 26 pins [form="♂ (shrouded male)"]
  X2 = shrouded pin header, 26 pins [form="♂ (shrouded male)"]
  Screwport_1 = screw terminal, 8 pins
  Keypad = screw terminal, 8 pins
  Screwport_2 = screw terminal, 4 pins
  LCD = screw terminal, 4 pins

nets:
  N1: Shield-Connector.A8, X2.pin3
  N2: Shield-Connector.A9, X2.pin24
  N3: Shield-Connector.A10, X2.pin4
  N4: Shield-Connector.A11, X2.pin23
  N5: Shield-Connector.A12, X2.pin5
  N6: Shield-Connector.A13, X2.pin22
  N7: Shield-Connector.A0, X1.pin2
  N8: Shield-Connector.A1, X1.pin25
  N9: Shield-Connector.A2, X1.pin3
  N10: Shield-Connector.A3, X1.pin24
  N11: Shield-Connector.A4, X1.pin4
  N12: Shield-Connector.A5, X1.pin23
  N13: Shield-Connector.A6, X2.pin2
  N14: Shield-Connector.A7, X2.pin25
  N15: Shield-Connector.D21/SCL, Shield-Connector.SCL, X1.pin10, Screwport_2.pin4, LCD.pin4
  N16: Shield-Connector.D20/SDA, Shield-Connector.SDA, X1.pin18, Screwport_2.pin3, LCD.pin3
  N17: Shield-Connector.D19/RX1, X1.pin22
  N18: Shield-Connector.D18/TX1, X1.pin5
  N19: Shield-Connector.D17_PWM/RX2, X2.pin12
  N20: Shield-Connector.D16_PWM/TX2, X2.pin16
  N21: Shield-Connector.AREF, X2.pin14
  N22: Shield-Connector.GND, X1.pin26, X2.pin13, X2.pin26, Screwport_2.pin1, LCD.pin1
  N23: Shield-Connector.D13_PWM, X2.pin9
  N24: Shield-Connector.D12_PWM, X2.pin19
  N25: Shield-Connector.D11_PWM, X2.pin8
  N26: Shield-Connector.D10_PWM, X2.pin20
  N27: Shield-Connector.D9_PWM, X2.pin7
  N28: Shield-Connector.D8_PWM, X2.pin21
  N29: Shield-Connector.RESET, X1.pin6, X2.pin6
  N30: Shield-Connector.3V3, X1.pin15, X2.pin15
  N31: Shield-Connector.5V, X1.pin1, X2.pin1, Screwport_2.pin2, LCD.pin2
  N32: Shield-Connector.D0_RX0, X1.pin14
  N33: Shield-Connector.D1_TX0, X1.pin13
  N34: Shield-Connector.D2_PWM, X1.pin21, Screwport_1.pin1, Keypad.pin1
  N35: Shield-Connector.D3_PWM, X1.pin7, Screwport_1.pin2, Keypad.pin2
  N36: Shield-Connector.D4_PWM, X1.pin20, Screwport_1.pin3, Keypad.pin3
  N37: Shield-Connector.D5_PWM, X1.pin8, Screwport_1.pin4, Keypad.pin4
  N38: Shield-Connector.D6_PWM, X1.pin19
  N39: Shield-Connector.D7_PWM, X1.pin9
  N40: Shield-Connector.D42, X2.pin18, Screwport_1.pin5, Keypad.pin5
  N41: Shield-Connector.D43, X2.pin10, Screwport_1.pin6, Keypad.pin6
  N42: Shield-Connector.D44, X2.pin17, Screwport_1.pin7, Keypad.pin7
  N43: Shield-Connector.D45, X2.pin11, Screwport_1.pin8, Keypad.pin8
  N44: Shield-Connector.D50, X1.pin16
  N45: Shield-Connector.D51, X1.pin11
  N46: Shield-Connector.D52, X1.pin12
  N47: Shield-Connector.D53, X1.pin17

notes:
  X1
  X2
  GND
  VCC
  SDA
  SCL
  AREF
  13
  12
  11
  10
  9
  8
  7
  6
  5
  4
  2
  RX0-0
  3
  TX0-1
  TX3-14
  RX3-15
  RX2-17
  TX2-16
  RX1-19
  TX1-18
  SDA-20
  SCL-21
  IOREF
  RESET
  5V
  3.3V
  Vin
  A4
  A6
  A5
  A2
  A0
  A3
  A1
  A7
  A15
  A12
  A14
  A13
  A11
  A10
  A9
  A8
  22
  24
  26
  27
  25
  23
  29
  34
  32
  30
  28
  46
  42
  50
  44
  48
  40
  38
  36
  52
  37
  41
  43
  31
  45
  39
  53
  35
  47
  49
  51
  33
  3V3
  -------------------
  CONTROLLINO-MAXI-ARDUINO-SHIELD-ADAPTOR
  version: v0.4 alpha
  date: 07.05.2016
  author: Florian Schulenburg
  David Niehaus
  revision: svn-r161
  C3
  C1
  C2
  R3
  R4
  R2
  R1
  C4
  www.arduino.cc
  www.controllino.biz
  www.fritzing.org
