# Fritzing sketch id1201_microcamera_0 (saved by Fritzing 0.8.7b)

parts:
  Arduino_UNO1 = Arduino
  J1 = male pin header, 3 pins [form="♂ (male)"]

nets:
  N1: Arduino_UNO1.connector3, J1.pin1
  N2: Arduino_UNO1.connector18, J1.pin3
  N3: Arduino_UNO1.connector19, J1.pin2
