# Fritzing sketch id1202_Untitled_Sketch_2_0 (saved by Fritzing 0.9.2b)
breadboards: 1

parts:
  M1 = DC Motor
  VCC1 = Battery block 9V
  Componente1 = Arduino Uno (Rev3)
  IC1 = H-Bridge [package=THT]
  S1 = Pushbutton [package="[THT]"]
  S2 = Pushbutton [package="[THT]"]
  R2 = Trimmer Potentiometer [maximum_resistance=10kΩ package=THT]
  R3 = Resistor [tolerance=±5% resistance=220 package=THT]
  R4 = Resistor [tolerance=±5% resistance=220 package=THT]

nets:
  N1: M1.pin_1, IC1.1Y
  N2: M1.pin_2, IC1.2Y
  N3: VCC1.-, IC1.VCC2
  N4: VCC1.+, R3.Pin_0, R4.Pin_0
  N5: Componente1.A0, R2.wiper
  N6: Componente1.D9_PWM, IC1.1_2EN
  N7: Componente1.D2, IC1.2A
  N8: Componente1.D3_PWM, IC1.1A
  N9: Componente1.D4, S2.Pin_1, S2.Pin_2, R4.Pin_1
  N10: Componente1.D5_PWM, S1.Pin_1, S1.Pin_2, R3.Pin_1
  N11: Componente1.5V, S1.Pin_3, S1.Pin_4, S2.Pin_3, S2.Pin_4, R2.leg1
  GND: Componente1.GND, IC1.GND1, IC1.GND2, IC1.VCC1, R2.leg2
