# Fritzing sketch id1203_cookieClickerScheme_0 (saved by Fritzing 0.8.5b)
breadboards: 3

parts:
  Part1 = Arduino Mega 2560 (Rev3)
  LCD1 = LCD screen
  S1 = Square Pushbutton
  S2 = Square Pushbutton
  S3 = Square Pushbutton
  S4 = Square Pushbutton
  S5 = Square Pushbutton
  S6 = Square Pushbutton
  LED2 = RGB LED (com. anode, rbg) [package="5 mm [THT]"]
  LED3 = RGB LED (com. anode, rbg) [package="5 mm [THT]"]
  LED4 = RGB LED (com. anode, rbg) [package="5 mm [THT]"]
  LED5 = RGB LED (com. anode, rbg) [package="5 mm [THT]"]
  U1 = POT [package=pot_alpha_rv16af-20]
  R1 = Resistor [tolerance=±5% resistance=220 package=THT]
  R2 = Resistor [tolerance=±5% resistance=220 package=THT]
  R3 = Resistor [tolerance=±5% resistance=220 package=THT]
  R4 = Resistor [tolerance=±5% resistance=220 package=THT]
  R5 = Resistor [tolerance=±5% resistance=220 package=THT]
  R6 = Resistor [tolerance=±1% resistance=220 package=THT]
  R7 = Resistor [tolerance=±5% resistance=220 package=THT]
  R8 = Resistor [tolerance=±5% resistance=220 package=THT]
  R9 = Resistor [tolerance=±5% resistance=220 package=THT]
  R10 = Resistor [tolerance=±5% resistance=220 package=THT]
  R11 = Resistor [tolerance=±5% resistance=220 package=THT]
  LED1 = RGB LED (com. anode, rbg) [package="5 mm [THT]"]

nets (from the schematic view):
  N1: Part1.D17_PWM/RX2, S4.leg1, R4.Pin_0
  N2: Part1.D16_PWM/TX2, R5.Pin_0
  N3: Part1.D15/RX3, S1.leg1, R6.Pin_0
  N4: Part1.GND, R4.Pin_1
  N5: Part1.D12_PWM, LCD1.RS
  N6: Part1.D11_PWM, LCD1.E
  5V: Part1.5V, LCD1.VSS, LCD1.R/W, LCD1.LED+, LCD1.LED-, S1.leg0, S2.leg0, S3.leg0, S4.leg0, S5.leg0, S6.leg0, U1.A, U1.E, R1.Pin_0, R2.Pin_1, R3.Pin_1, R6.Pin_1
  N7: Part1.D6_PWM, S6.leg1, R1.Pin_1
  N8: Part1.D7_PWM, S2.leg1, R2.Pin_0
  N9: Part1.D42, LED5.red_cathode
  N10: Part1.D43, LED5.green_cathode
  N11: Part1.D44, LED4.red_cathode
  N12: Part1.D46, LED3.red_cathode
  N13: Part1.D47, LED3.green_cathode
  N14: Part1.D48, LED2.red_cathode
  N15: Part1.D49, LED2.green_cathode
  N16: Part1.D50, LED1.red_cathode
  N17: Part1.D51, LED1.green_cathode
  N18: LCD1.V0, U1.S
  N19: S3.leg1, R3.Pin_0
  N20: LED2.common_anode, R8.Pin_0
  N21: LED3.common_anode, R9.Pin_0
  N22: LED4.common_anode, R10.Pin_0
  N23: LED5.common_anode, R11.Pin_0
  N24: R7.Pin_0, LED1.common_anode
