# Fritzing sketch id1204_circuit_0 (saved by Fritzing 0.9.2b)
breadboards: 1

parts:
  Q2 = Basic FET N-Channel [package="TO220 [THT]"]
  Q1 = Basic FET N-Channel [package="TO220 [THT]"]
  ESP8266-1 = ESP8266-12-Breakout [part_number=ESP8266-12]
  DS1 = DS18B20_1_Wire_Temperature_Sensor [part_number=DS18B20]  # not connected
  DS2 = DS18B20_1_Wire_Temperature_Sensor [part_number=DS18B20]  # not connected
  DS3 = DS18B20_1_Wire_Temperature_Sensor [part_number=DS18B20]  # not connected

nets:
  N1: Q2.drain, ESP8266-1.connector12
  N2: Q2.source, Q1.source
  N3: Q1.drain, ESP8266-1.connector11
