# Fritzing sketch id1205_CoolerFritzing_0 (saved by Fritzing 0.9.2b)
breadboards: 1

parts:
  M1 = DC Motor
  Part1 = Arduino Uno (Rev3) - ICSP
  Q1 = PNP-Transistor [package="TO92 [THT]"]
  J1 = Basic Servo
  J2 = Basic Servo
  J3 = Basic Servo

nets:
  GND: M1.pin_1, Part1.GND, J1.gnd, J2.gnd, J3.gnd
  N1: M1.pin_2, Q1.C
  N2: Part1.D12/MISO, J3.pulse
  N3: Part1.D13/SCK, J2.pulse
  N4: Part1.D6_PWM, J1.pulse
  N5: Part1.D7, Q1.B
  VCC: Part1.5V, Q1.E, J1.vcc, J2.vcc, J3.vcc

notes:
  Outputs from rasberry pi
  Just have motor connected to arduino power for convenience right now
  Soda1
  Soda2
  Soda3
