# Fritzing sketch id1206_Cooling_Pad_PCB_0 (saved by Fritzing 0.9.3b)
circuit board: 13.3464cm x 5.74689cm
breadboards: 1

parts:
  14m2 = PICAXE-14M [package=THT]
  Stuart_Cumming_Cooling_Fan = female pin header, 2 pins [form="♀ (female)"]
  Small_Fans = female pin header, 2 pins [form="♀ (female)"]
  27/07/2017 = female pin header, 2 pins [form="♀ (female)"]
  Pcb_#1 = female pin header, 2 pins [form="♀ (female)"]
  Fan = female pin header, 2 pins [form="♀ (female)"]
  Yellow = female pin header, 2 pins [form="♀ (female)"]
  Red = female pin header, 2 pins [form="♀ (female)"]
  Power = female pin header, 2 pins [form="♀ (female)"]
  Green = female pin header, 2 pins [form="♀ (female)"]
  5V_In = female pin header, 2 pins [form="♀ (female)"]
  180 = Resistor [tolerance=±5% resistance=220 package=THT]
  R2 = Resistor [tolerance=±5% resistance=220 package=THT]
  180_2 = Resistor [tolerance=±5% resistance=220 package=THT]
  180_3 = Resistor [tolerance=±5% resistance=220 package=THT]
  R5 = Resistor [tolerance=±5% resistance=220 package=THT]
  Switch = female pin header, 2 pins [form="♀ (female)"]
  4k7 = Resistor [tolerance=±5% resistance=220 package=THT]
  DTS = female pin header, 3 pins [form="♀ (female)"]
  Q1 = NPN-Transistor [package="TO92 [THT]"]
  Q2 = NPN-Transistor [package="TO92 [THT]"]
  1k = Resistor [tolerance=±5% resistance=220 package=THT]
  1k_2 = Resistor [tolerance=±5% resistance=220 package=THT]
  9V = female pin header, 2 pins [form="♀ (female)"]
  Off_Led = female pin header, 2 pins [form="♀ (female)"]
  J2 = female pin header, 2 pins [form="♀ (female)"]
  R6 = Resistor [tolerance=±5% resistance=220 package=THT]
  R7 = Resistor [tolerance=±5% resistance=220 package=THT]
  J3 = female pin header, 1 pin [form="♀ (female)"]
  J4 = female pin header, 1 pin [form="♀ (female)"]
  J5 = female pin header, 1 pin [form="♀ (female)"]
  J6 = female pin header, 1 pin [form="♀ (female)"]
  J7 = female pin header, 1 pin [form="♀ (female)"]
  J8 = female pin header, 1 pin [form="♀ (female)"]
  J9 = female pin header, 1 pin [form="♀ (female)"]
  J10 = female pin header, 1 pin [form="♀ (female)"]
  J11 = female pin header, 1 pin [form="♀ (female)"]
  J12 = female pin header, 1 pin [form="♀ (female)"]

nets:
  N1: 14m2.+V, 5V_In.pin2, R2.Pin_1, Switch.pin1, 4k7.Pin_0, DTS.pin2, J4.pin1, J6.pin1
  N2: 14m2.In_4_/_ADC_4, 4k7.Pin_1, DTS.pin1
  N3: 14m2.In_1, 1k_2.Pin_0
  N4: 14m2.In_0_/_ADC_0, R5.Pin_1, Switch.pin2
  N5: 14m2.Out_4, 1k.Pin_0
  N6: 14m2.Out_3, 180.Pin_1
  N7: 14m2.Out_2, 180_3.Pin_1
  N8: 14m2.Out_1, 180_2.Pin_1
  N9: 14m2.0V, Stuart_Cumming_Cooling_Fan.pin1, Small_Fans.pin1, 27/07/2017.pin1, Pcb_#1.pin1, Fan.pin1, Yellow.pin2, Red.pin2, Power.pin2, Green.pin2, 5V_In.pin1, R5.Pin_0, DTS.pin3, Q1.C, Q2.C, 9V.pin2, Off_Led.pin1, J2.pin1
  N10: Stuart_Cumming_Cooling_Fan.pin2, Small_Fans.pin2, 27/07/2017.pin2, Pcb_#1.pin2, J5.pin1
  N11: Fan.pin2, J11.pin1
  N12: Yellow.pin1, 180_3.Pin_0
  N13: Red.pin1, 180_2.Pin_0
  N14: Power.pin1, R2.Pin_0
  N15: Green.pin1, 180.Pin_0
  N16: Q1.E, J9.pin1
  N17: Q1.B, 1k_2.Pin_1
  N18: Q2.E, J8.pin1
  N19: Q2.B, 1k.Pin_1
  N20: 9V.pin1, J7.pin1, J12.pin1
  N21: Off_Led.pin2, R7.Pin_1
  N22: J2.pin2, R6.Pin_1
  N23: R6.Pin_0, J10.pin1
  N24: R7.Pin_0, J3.pin1

notes:
  Stuart Cumming Cooling Fan PCB
  7/08/2017
  PCB #1
  L
  Small Fans
  14m2
  180
  LED
  Green
  Yellow
  RED
  1K
  RELAY
  4K7
  9V
  5V
  Power
  DTS
  10K
  Switch
