# Fritzing sketch id1207_coolometer_0 (saved by Fritzing 0.9.2b)
circuit board: 6.43646cm x 6.05574cm
perfboards: 1

parts:
  MV1 = MicroView [part_number=MicroView]
  C1 = Ceramic Capacitor [capacitance=100nF package="100 mil [THT, multilayer]"]
  U1 = OP27 - Low Noise, Precision Op Amp [part_number=CA3140]
  R2 = Resistor [tolerance=±5% resistance=68 package=THT]
  R3 = Resistor [tolerance=±5% resistance=220 package=THT]
  R1 = Resistor [tolerance=±5% resistance=12 package=THT]
  Q1 = PNP-Transistor [part_number=BC327-25 package="TO92 [THT]"]
  Q2 = PNP-Transistor [part_number=BC327-25 package="TO92 [THT]"]
  C2 = Ceramic Capacitor [capacitance=100nF package="100 mil [THT, multilayer]"]
  J1 = female pin header, 7 pins [form="♀ (female)"]
  J2 = female pin header, 7 pins [form="♀ (female)"]
  J3 = female pin header, 5 pins [form="♀ (female)"]
  VR1 = Trimmer Potentiometer [maximum_resistance=10kΩ package=THT]
  VR2 = Trimmer Potentiometer [maximum_resistance=10kΩ package=THT]
  S1 = Pushbutton [package="[THT]"]

nets:
  N1: MV1.connector0, C1.0
  N2: MV1.connector1, S1.Pin_1, S1.Pin_2
  N3: MV1.connector5, R1.Pin_0, Q2.C, VR1.leg2
  N4: MV1.connector6, U1.+IN, R1.Pin_1, J3.pin1
  N5: MV1.connector7, U1.-V, Q1.C, C2.0, J1.pin7, J3.pin5, VR1.leg1, VR2.wiper
  N6: MV1.connector8, J1.pin1
  N7: MV1.connector9, J1.pin5
  N8: MV1.connector14, U1.V+, R2.Pin_0, Q2.E, C2.1, J1.pin4
  N9: C1.1, J1.pin2
  N10: U1.TRIM#1, VR2.leg1
  N11: U1.-IN, VR1.wiper
  N12: U1.NC, VR2.leg2
  N13: U1.OUT, Q1.B
  N14: R2.Pin_1, R3.Pin_0, Q2.B
  N15: R3.Pin_1, Q1.E
  N16: J2.pin1, S1.Pin_3, S1.Pin_4
