# Fritzing sketch id120_4In_4Out_I2C_1Wire_0 (saved by Fritzing 0.8.7b)
circuit board: 6.9215cm x 5.33756cm
breadboards: 2

parts:
  U1 = Optocoupler [package=THT]
  U2 = Optocoupler [package=THT]
  U3 = Optocoupler [package=THT]
  U4 = Optocoupler [package=THT]
  R1 = Resistor [resistance=270 tolerance=±5% package=THT]
  R2 = Resistor [resistance=270 tolerance=±5% package=THT]
  R3 = Resistor [resistance=270 tolerance=±5% package=THT]
  R4 = Resistor [resistance=270 tolerance=±5% package=THT]
  R5 = Resistor [resistance=2.2k tolerance=±5% package=THT]
  R6 = Resistor [resistance=2.2k tolerance=±5% package=THT]
  R7 = Resistor [resistance=2.2k tolerance=±5% package=THT]
  R8 = Resistor [resistance=2.2k tolerance=±5% package=THT]
  K1 = Relay [part_number=FRS1B-S package=THT]
  K2 = Relay [part_number=FRS1B-S package=THT]
  K3 = Relay [part_number=FRS1B-S package=THT]
  K4 = Relay [part_number=FRS1B-S package=THT]
  Q1 = NPN-Transistor [part_number=2N3904 package="TO92 [THT]"]
  Q2 = NPN-Transistor [part_number=2N3904 package="TO92 [THT]"]
  Q3 = NPN-Transistor [part_number=2N3904 package="TO92 [THT]"]
  Q4 = NPN-Transistor [part_number=2N3904 package="TO92 [THT]"]
  R9 = Resistor [resistance=330 tolerance=±5% package=THT]
  R10 = Resistor [resistance=330 tolerance=±5% package=THT]
  R11 = Resistor [resistance=330 tolerance=±5% package=THT]
  R12 = Resistor [resistance=330 tolerance=±5% package=THT]
  D2 = Rectifier Diode [part_number=1N4001 package="300 mil [THT]"]
  D3 = Rectifier Diode [part_number=1N4001 package="300 mil [THT]"]
  D4 = Rectifier Diode [part_number=1N4001 package="300 mil [THT]"]
  D1 = Rectifier Diode [part_number=1N4001 package="300 mil [THT]"]
  J4 = Screw terminal - 2 pins [package=THT]
  J3 = Screw terminal - 2 pins [package=THT]
  J2 = Screw terminal - 2 pins [package=THT]
  J1 = Screw terminal - 2 pins [package=THT]
  J5 = Screw terminal - 2 pins [package=THT]
  J6 = Screw terminal - 2 pins [package=THT]
  J7 = Screw terminal - 2 pins [package=THT]
  J8 = Screw terminal - 2 pins [package=THT]
  R18 = Resistor [tolerance=±5% resistance=220 package=THT]
  LED10 = LED - 3mm [color="Green (555nm)" package="3 mm [THT]"]
  Arduino1 = Arduino
  R20 = Resistor [tolerance=±5% resistance=2.2k package=THT]
  R21 = Resistor [tolerance=±5% resistance=2.2k package=THT]
  LED1 = LED - 3mm [color="Red (633nm)" package="3 mm [THT]"]
  LED2 = LED - 3mm [color="Red (633nm)" package="3 mm [THT]"]
  LED3 = LED - 3mm [color="Red (633nm)" package="3 mm [THT]"]
  LED4 = LED - 3mm [color="Red (633nm)" package="3 mm [THT]"]
  LED5 = LED - 3mm [color="Red (633nm)" package="3 mm [THT]"]
  LED6 = LED - 3mm [color="Red (633nm)" package="3 mm [THT]"]
  LED7 = LED - 3mm [color="Red (633nm)" package="3 mm [THT]"]
  LED8 = LED - 3mm [color="Red (633nm)" package="3 mm [THT]"]
  J11 = screw terminal, 3 pins

nets:
  N1: U1.Pin_1, LED4.cathode
  GND: U1.Pin_2, U1.Pin_4, U2.Pin_2, U2.Pin_4, U3.Pin_2, U3.Pin_4, U4.Pin_2, U4.Pin_4, R5.Pin_1, R6.Pin_1, R7.Pin_1, R8.Pin_1, Q1.E, Q2.E, Q3.E, Q4.E, LED10.cathode, Arduino1.GND, J11.pin2
  N2: U1.Pin_5, Arduino1.D9
  N3: U2.Pin_1, LED3.cathode
  N4: U2.Pin_5, Arduino1.D8
  N5: U3.Pin_1, LED2.cathode
  N6: U3.Pin_5, Arduino1.D7
  N7: U4.Pin_1, LED1.cathode
  N8: U4.Pin_5, Arduino1.D6
  N9: R1.Pin_0, J4.pin2
  N10: R1.Pin_1, R5.Pin_0, LED4.anode
  N11: R2.Pin_0, J3.pin2
  N12: R2.Pin_1, R6.Pin_0, LED3.anode
  N13: R3.Pin_0, J2.pin2
  N14: R3.Pin_1, R7.Pin_0, LED2.anode
  N15: R4.Pin_0, J1.pin2
  N16: R4.Pin_1, R8.Pin_0, LED1.anode
  N17: K1.COIL1, K2.COIL1, K3.COIL2, K4.COIL2, D2.cathode, D3.cathode, D4.cathode, D1.cathode, J4.pin1, J3.pin1, J2.pin1, J1.pin1, Arduino1.+5V, R20.Pin_0, R21.Pin_1
  N18: K1.C1, K1.C2, J8.pin2
  N19: K1.COIL2, Q1.C, D3.anode
  N20: K1.B, J8.pin1
  N21: K2.C1, K2.C2, J5.pin1
  N22: K2.COIL2, Q3.C, D4.anode
  N23: K2.B, J5.pin2
  N24: K3.COIL1, Q4.C, D1.anode
  N25: K3.C1, K3.C2, J6.pin1
  N26: K3.B, J6.pin2
  N27: K4.COIL1, Q2.C, D2.anode
  N28: K4.C1, K4.C2, J7.pin2
  N29: K4.B, J7.pin1
  N30: Q1.B, LED7.cathode
  N31: Q2.B, LED8.cathode
  N32: Q3.B, LED6.cathode
  N33: Q4.B, LED5.cathode
  N34: R9.Pin_0, LED5.anode
  N35: R9.Pin_1, Arduino1.D2
  N36: R10.Pin_0, LED6.anode
  N37: R10.Pin_1, Arduino1.D3
  N38: R11.Pin_0, LED7.anode
  N39: R11.Pin_1, Arduino1.D5
  N40: R12.Pin_0, LED8.anode
  N41: R12.Pin_1, Arduino1.A0
  N42: R18.Pin_0, LED10.anode
  N43: R18.Pin_1, Arduino1.A1
  N44: Arduino1.A4, R20.Pin_1, J11.pin3
  N45: Arduino1.A5, R21.Pin_0, J11.pin1

notes:
  4 E/S
  by GJ
  01
  02
  03
  04
  SCL-SDA
  Digital M2M
  HB
