# Fritzing sketch id121_Leds_0 (saved by Fritzing 0.9.3b)
circuit board: 4.65cm x 4.65cm
breadboards: 1

parts:
  Part1 = Arduino Nano (Rev3.0)
  LED4 = LED - 5mm [color="Green (570nm)" package="5 mm [THT]"]
  LED3 = LED - 5mm [color="Green (570nm)" package="5 mm [THT]"]
  LED2 = LED - 5mm [color="Green (570nm)" package="5 mm [THT]"]
  LED1 = LED - 5mm [color="Green (570nm)" package="5 mm [THT]"]
  R2 = Resistor [tolerance=±5% resistance=220 package="1206 [SMD]"]
  R3 = Resistor [tolerance=±5% resistance=220 package="1206 [SMD]"]
  R4 = Resistor [tolerance=±5% resistance=220 package="1206 [SMD]"]
  R5 = Resistor [tolerance=±5% resistance=220 package="1206 [SMD]"]

nets:
  N1: Part1.GND, LED4.anode, LED3.anode, LED2.anode, LED1.anode
  N2: Part1.D9, R5.Pin_1
  N3: Part1.D10, R2.Pin_1
  N4: Part1.D11/MOSI, R3.Pin_1
  N5: Part1.D12/MISO, R4.Pin_1
  N6: LED4.cathode, R4.Pin_0
  N7: LED3.cathode, R3.Pin_0
  N8: LED2.cathode, R2.Pin_0
  N9: LED1.cathode, R5.Pin_0
