# Fritzing sketch id122_4_led_0 (saved by Fritzing 0.9.2b)
breadboards: 1

parts:
  Onderdeel1 = Arduino Uno (Rev3)
  LED1 = LED - 5mm [color="Red (633nm)" package="5 mm [THT]"]
  R1 = Resistor [tolerance=±5% resistance=220 package=THT]
  LED2 = LED - 5mm [color="Red (633nm)" package="5 mm [THT]"]
  LED3 = LED - 5mm [color="Red (633nm)" package="5 mm [THT]"]
  LED4 = LED - 5mm [color="Red (633nm)" package="5 mm [THT]"]
  R2 = Resistor [tolerance=±5% resistance=220 package=THT]
  R3 = Resistor [tolerance=±5% resistance=220 package=THT]
  R4 = Resistor [tolerance=±5% resistance=220 package=THT]
  S1 = Pushbutton [package="[THT]"]
  R5 = Resistor [tolerance=±5% resistance=220 package=THT]

nets:
  N1: Onderdeel1.GND, R1.Pin_0, S1.Pin_3, S1.Pin_4
  N2: Onderdeel1.D2, LED4.anode
  N3: Onderdeel1.D3_PWM, LED3.anode
  N4: Onderdeel1.D4, LED2.anode
  N5: Onderdeel1.D5_PWM, LED1.anode
  N6: Onderdeel1.D7, S1.Pin_1, S1.Pin_2, R5.Pin_0
  N7: LED1.cathode, R1.Pin_1
  N8: LED2.cathode, R2.Pin_1
  N9: LED3.cathode, R3.Pin_1
  N10: LED4.cathode, R4.Pin_0
  N11: R2.Pin_0, R3.Pin_0, R4.Pin_1, R5.Pin_1
