# Fritzing sketch id1231_project_one_diagram_0 (saved by Fritzing 0.9.3b)
circuit board: 8.46667cm x 5.64444cm
breadboards: 1

parts:
  Part1 = Arduino Uno (Rev3)
  U1 = LCD-16X2 [package=lcd-16x2_noholes]
  U2 = POT [package=3362u]
  LED1 = RGB LED (com. cathode, rgb) [package="5 mm [THT]"]
  R1 = Resistor [tolerance=±5% resistance=220 package=THT]
  R2 = Resistor [tolerance=±5% resistance=220 package=THT]
  R3 = Resistor [tolerance=±5% resistance=220 package=THT]
  S1 = Pushbutton [package="[THT]"]
  R4 = Resistor [tolerance=±5% resistance=220 package="2512 [SMD]"]
  Part2 = Ambient Light Sensor (TEMT6000 Breakout Board)

nets:
  N1: Part1.A0, Part2.S
  N2: Part1.D8, R1.Pin_1
  N3: Part1.D9_PWM, R3.Pin_1
  N4: Part1.D10_PWM/SS, R2.Pin_1
  N5: Part1.D11_PWM/MOSI, U1.E
  N6: Part1.D12/MISO, U1.RS
  N7: Part1.D13/SCK, S1.Pin_3, S1.Pin_4, R4.Pin_0
  N8: Part1.D2, U1.DB7
  N9: Part1.D3_PWM, U1.DB6
  N10: Part1.D4, U1.DB5
  N11: Part1.D5_PWM, U1.DB4
  5V: Part1.5V, U1.VDD, U1.K, U2.E, S1.Pin_1, S1.Pin_2, Part2.VCC
  GND: Part1.GND, U1.VSS, U1.R_W, U1.A, U2.A, LED1.common_cathode, R4.Pin_1, Part2.GND
  N12: U1.VO, U2.S
  N13: LED1.red_anode, R3.Pin_0
  N14: LED1.green_anode, R2.Pin_0
  N15: LED1.blue_anode, R1.Pin_0
