# Fritzing sketch id1232_miniRayGun_0 (saved by Fritzing 0.6.4b)
breadboards: 1

parts:
  R1 = Resistor [resistance=220 tolerance=±5% package=THT]
  R1_2 = Resistor [resistance=220 tolerance=±5% package=THT]
  Button = Pushbutton [package=THT]
  R2 = Resistor [resistance=1k tolerance=±5% package=THT]
  Speaker = Piezo Speaker
  J2 = female pin header, 6 pins [form="♂ (male)"]
  LOADING = green LED - 5mm [package="5 mm [THT]"]
  LED = yellow LED - 5mm [package="5 mm [THT]"]

nets:
  N1: R1.Pin_0, J2.pin3
  N2: R1.Pin_1, LED.anode
  N3: R1_2.Pin_0, J2.pin1
  N4: R1_2.Pin_1, LOADING.anode
  N5: Button.leg0, J2.pin2
  N6: Button.leg1, R2.Pin_1, J2.pin6
  N7: R2.Pin_0, Speaker.pin1, J2.pin4, LOADING.cathode, LED.cathode
  N8: Speaker.pin2, J2.pin5

notes:
  fab.fritzing.org
