# Fritzing sketch id1233_planter_0 (saved by Fritzing 0.9.3b)
stripboards: 1

parts:
  MCU1 = Raspberry Pi Zero
  Part2 = adafruit
  Part3 = PAM8302A
  SPKR1 = Loudspeaker
  U1 = mystery part, 40 pins

nets:
  N1: MCU1.pin_2, MCU1.pin_4, Part2.connector13, Part3.connector17, U1.pin1
  N2: MCU1.pin_3, Part2.connector17
  N3: MCU1.pin_5, Part2.connector16
  N4: MCU1.pin_6, MCU1.pin_34, Part2.connector15, Part3.connector16, Part3.connector19, U1.pin3
  N5: MCU1.pin_12, Part3.connector20
  N6: MCU1.pin_16, U1.pin9
  N7: MCU1.pin_18, U1.pin8
  N8: Part3.connector40, SPKR1.pin2
  N9: Part3.connector41, SPKR1.pin1

notes:
  5v
  Ground
