# Fritzing sketch id1234_test12345_0 (saved by Fritzing 0.9.0b)
circuit board: 25.2773cm x 12.1373cm
breadboards: 1

parts:
  U5 = IC4081
  LED1 = LED - 5mm [color="Red (633nm)" package="5 mm [THT]"]
  LED2 = LED - 5mm [color="Red (633nm)" package="5 mm [THT]"]
  LED3 = LED - 5mm [color="Red (633nm)" package="5 mm [THT]"]
  LED4 = LED - 5mm [color="Red (633nm)" package="5 mm [THT]"]
  LED5 = LED - 5mm [color="Red (633nm)" package="5 mm [THT]"]
  LED6 = LED - 5mm [color="Red (633nm)" package="5 mm [THT]"]
  LED7 = LED - 5mm [color="Red (633nm)" package="5 mm [THT]"]
  LED8 = LED - 5mm [color="Red (633nm)" package="5 mm [THT]"]
  LED9 = LED - 5mm [color="Red (633nm)" package="5 mm [THT]"]
  LED10 = LED - 5mm [color="Red (633nm)" package="5 mm [THT]"]
  LED17 = LED - 5mm [color="Red (633nm)" package="5 mm [THT]"]
  LED16 = LED - 5mm [color="Red (633nm)" package="5 mm [THT]"]
  LED14 = LED - 5mm [color="Red (633nm)" package="5 mm [THT]"]
  LED15 = LED - 5mm [color="Red (633nm)" package="5 mm [THT]"]
  LED11 = LED - 5mm [color="Red (633nm)" package="5 mm [THT]"]
  LED12 = LED - 5mm [color="Red (633nm)" package="5 mm [THT]"]
  LED13 = LED - 5mm [color="Red (633nm)" package="5 mm [THT]"]
  R1 = Resistor [tolerance=±5% resistance=470 package="0805 [SMD]"]
  R2 = Resistor [tolerance=±5% resistance=470 package="0805 [SMD]"]
  R3 = Resistor [tolerance=±5% resistance=470 package="0805 [SMD]"]
  R4 = Resistor [tolerance=±5% resistance=470 package="0805 [SMD]"]
  R5 = Resistor [tolerance=±5% resistance=470 package="0805 [SMD]"]
  R6 = Resistor [tolerance=±5% resistance=470 package="0805 [SMD]"]
  R7 = Resistor [tolerance=±5% resistance=470 package="0805 [SMD]"]
  R8 = Resistor [tolerance=±5% resistance=470 package="0805 [SMD]"]
  R9 = Resistor [tolerance=±5% resistance=470 package="0805 [SMD]"]
  R10 = Resistor [tolerance=±5% resistance=470 package="0805 [SMD]"]
  R11 = Resistor [tolerance=±5% resistance=470 package="0805 [SMD]"]
  R12 = Resistor [tolerance=±5% resistance=470 package="0805 [SMD]"]
  R13 = Resistor [tolerance=±5% resistance=470 package="0805 [SMD]"]
  R14 = Resistor [tolerance=±5% resistance=470 package="0805 [SMD]"]
  R15 = Resistor [tolerance=±5% resistance=470 package="0805 [SMD]"]
  R16 = Resistor [tolerance=±5% resistance=470 package="0805 [SMD]"]
  R17 = Resistor [tolerance=±5% resistance=470 package="0805 [SMD]"]
  U6 = IC4017-2
  U7 = IC4017-2
  S1 = SWITCH-MOMENTARY-2 [package=tactile-pth-12mm]
  C1 = Ceramic Capacitor [capacitance=100nF package="100 mil [THT, multilayer]"]
  VCC1 = Battery block 9V
  R19 = Resistor [tolerance=±5% resistance=10k package=THT]

nets:
  N1: U5.connector0, U6.connector10, U6.connector12
  N2: U5.connector1, U6.connector13, S1.2, C1.0, R19.Pin_0
  N3: U5.connector2, U7.connector13
  N4: U5.connector12, U6.connector15, U7.connector15, S1.1, C1.1, VCC1.+
  N5: U5.connector13, LED1.cathode, LED2.cathode, LED3.cathode, LED4.cathode, LED5.cathode, LED6.cathode, LED7.cathode, LED8.cathode, LED9.cathode, LED10.cathode, LED17.cathode, LED16.cathode, LED14.cathode, LED15.cathode, LED11.cathode, LED12.cathode, LED13.cathode, U6.connector7, U7.connector7, U7.connector12, VCC1.-, R19.Pin_1
  N6: LED1.anode, R1.Pin_1
  N7: LED2.anode, R2.Pin_1
  N8: LED3.anode, R3.Pin_1
  N9: LED4.anode, R4.Pin_1
  N10: LED5.anode, R5.Pin_1
  N11: LED6.anode, R6.Pin_1
  N12: LED7.anode, R7.Pin_1
  N13: LED8.anode, R8.Pin_1
  N14: LED9.anode, R9.Pin_1
  N15: LED10.anode, R10.Pin_1
  N16: LED17.anode, R17.Pin_1
  N17: LED16.anode, R16.Pin_1
  N18: LED14.anode, R14.Pin_1
  N19: LED15.anode, R15.Pin_1
  N20: LED11.anode, R11.Pin_1
  N21: LED12.anode, R12.Pin_1
  N22: LED13.anode, R13.Pin_1
  N23: R1.Pin_0, U6.connector2, U7.connector14
  N24: R2.Pin_0, U6.connector1
  N25: R3.Pin_0, U6.connector3
  N26: R4.Pin_0, U6.connector6
  N27: R5.Pin_0, U6.connector9
  N28: R6.Pin_0, U6.connector0
  N29: R7.Pin_0, U6.connector4
  N30: R8.Pin_0, U6.connector5
  N31: R9.Pin_0, U6.connector8
  N32: R10.Pin_0, U7.connector1
  N33: R11.Pin_0, U7.connector3
  N34: R12.Pin_0, U7.connector6
  N35: R13.Pin_0, U7.connector9
  N36: R14.Pin_0, U7.connector0
  N37: R15.Pin_0, U7.connector4
  N38: R16.Pin_0, U7.connector5
  N39: R17.Pin_0, U7.connector8
  N40: U6.connector14, U7.connector10
