# Fritzing sketch id1235_Chrono_Big_Digit_0 (saved by Fritzing 0.9.2b)
circuit board: 20.5839cm x 10.8727cm
breadboards: 1

parts:
  LED2 = LED - 5mm [color="Red (633nm)" package="5 mm [THT]"]
  U1 = 74HC595 [package="DIP16 [THT]"]
  R1 = Resistor [tolerance=±5% resistance=220 package=THT]
  R2 = Resistor [tolerance=±5% resistance=220 package=THT]
  R3 = Resistor [tolerance=±5% resistance=220 package=THT]
  R4 = Resistor [tolerance=±5% resistance=220 package=THT]
  R5 = Resistor [tolerance=±5% resistance=220 package=THT]
  R6 = Resistor [tolerance=±5% resistance=220 package=THT]
  R7 = Resistor [tolerance=±5% resistance=220 package=THT]
  LED4 = LED - 5mm [color="Red (633nm)" package="5 mm [THT]"]
  U7 = 74HC595 [package="DIP16 [THT]"]
  U9 = 74HC595 [package="DIP16 [THT]"]
  U10 = 74HC595 [package="DIP16 [THT]"]
  R172 = Resistor [tolerance=±5% resistance=330 package=THT]
  R173 = Resistor [tolerance=±5% resistance=330 package=THT]
  R177 = Resistor [tolerance=±5% resistance=150 package=THT]
  LED10 = LED - 3mm [color="Red (633nm)" package="3 mm [THT]"]
  J1 = female pin header, 7 pins [form="♀ (female)"]
  Minute_Tens = TOA-23101DMRL-B
  Minute_Units = TOA-23101DMRL-B
  R185 = Resistor [tolerance=±5% resistance=220 package=THT]
  R186 = Resistor [tolerance=±5% resistance=220 package=THT]
  R187 = Resistor [tolerance=±5% resistance=220 package=THT]
  R188 = Resistor [tolerance=±5% resistance=220 package=THT]
  R189 = Resistor [tolerance=±5% resistance=220 package=THT]
  R190 = Resistor [tolerance=±5% resistance=220 package=THT]
  R191 = Resistor [tolerance=±5% resistance=220 package=THT]
  Second_Tens = TOA-23101DMRL-B
  R192 = Resistor [tolerance=±5% resistance=220 package=THT]
  R193 = Resistor [tolerance=±5% resistance=220 package=THT]
  R194 = Resistor [tolerance=±5% resistance=220 package=THT]
  R195 = Resistor [tolerance=±5% resistance=220 package=THT]
  R196 = Resistor [tolerance=±5% resistance=220 package=THT]
  R197 = Resistor [tolerance=±5% resistance=220 package=THT]
  R198 = Resistor [tolerance=±5% resistance=220 package=THT]
  R178 = Resistor [tolerance=±5% resistance=220 package=THT]
  R179 = Resistor [tolerance=±5% resistance=220 package=THT]
  R182 = Resistor [tolerance=±5% resistance=220 package=THT]
  Second_Units = TOA-23101DMRL-B
  R183 = Resistor [tolerance=±5% resistance=220 package=THT]
  R180 = Resistor [tolerance=±5% resistance=220 package=THT]
  R184 = Resistor [tolerance=±5% resistance=220 package=THT]
  R181 = Resistor [tolerance=±5% resistance=220 package=THT]

nets:
  N1: LED2.cathode, R173.Pin_1
  N2: LED2.anode, LED4.anode, J1.pin2
  N3: U1.Q1, R2.Pin_0
  N4: U1.Q2, R3.Pin_0
  N5: U1.Q3, R4.Pin_0
  N6: U1.Q4, R5.Pin_0
  N7: U1.Q5, R6.Pin_0
  N8: U1.Q6, R7.Pin_0
  GND: U1.GND, U1.OE, U7.GND, U7.OE, U9.GND, U9.OE, U10.GND, U10.OE, R172.Pin_0, R173.Pin_0, R177.Pin_1, J1.pin4
  N9: U1.Q7', U7.DS
  VCC: U1.MR, U1.VCC, U7.MR, U7.VCC, U9.MR, U9.VCC, U10.MR, U10.VCC, LED10.anode, J1.pin7
  N10: U1.SH_CP, U7.SH_CP, U9.SH_CP, U10.SH_CP, J1.pin6
  N11: U1.ST_CP, U7.ST_CP, U9.ST_CP, U10.ST_CP, J1.pin5
  N12: U1.DS, J1.pin3
  N13: U1.Q0, R1.Pin_0
  N14: R1.Pin_1, Minute_Tens.connector7
  N15: R2.Pin_1, Minute_Tens.connector6
  N16: R3.Pin_1, Minute_Tens.connector4
  N17: R4.Pin_1, Minute_Tens.connector2
  N18: R5.Pin_1, Minute_Tens.connector1
  N19: R6.Pin_1, Minute_Tens.connector9
  N20: R7.Pin_1, Minute_Tens.connector10
  N21: LED4.cathode, R172.Pin_1
  N22: U7.Q1, R190.Pin_0
  N23: U7.Q2, R189.Pin_0
  N24: U7.Q3, R188.Pin_0
  N25: U7.Q4, R187.Pin_0
  N26: U7.Q5, R186.Pin_0
  N27: U7.Q6, R185.Pin_0
  N28: U7.Q7', U9.DS
  N29: U7.Q0, R191.Pin_0
  N30: U9.Q1, R197.Pin_0
  N31: U9.Q2, R196.Pin_0
  N32: U9.Q3, R195.Pin_0
  N33: U9.Q4, R194.Pin_0
  N34: U9.Q5, R193.Pin_0
  N35: U9.Q6, R192.Pin_0
  N36: U9.Q7', U10.DS
  N37: U9.Q0, R198.Pin_0
  N38: U10.Q1, R183.Pin_0
  N39: U10.Q2, R182.Pin_0
  N40: U10.Q3, R181.Pin_0
  N41: U10.Q4, R180.Pin_0
  N42: U10.Q5, R179.Pin_0
  N43: U10.Q6, R178.Pin_0
  N44: U10.Q0, R184.Pin_0
  N45: R177.Pin_0, LED10.cathode
  N46: J1.pin1, Minute_Tens.connector3, Minute_Units.connector3, Second_Tens.connector3, Second_Units.connector3
  N47: Minute_Units.connector1, R187.Pin_1
  N48: Minute_Units.connector2, R188.Pin_1
  N49: Minute_Units.connector4, R189.Pin_1
  N50: Minute_Units.connector6, R190.Pin_1
  N51: Minute_Units.connector7, R191.Pin_1
  N52: Minute_Units.connector9, R186.Pin_1
  N53: Minute_Units.connector10, R185.Pin_1
  N54: Second_Tens.connector1, R194.Pin_1
  N55: Second_Tens.connector2, R195.Pin_1
  N56: Second_Tens.connector4, R196.Pin_1
  N57: Second_Tens.connector6, R197.Pin_1
  N58: Second_Tens.connector7, R198.Pin_1
  N59: Second_Tens.connector9, R193.Pin_1
  N60: Second_Tens.connector10, R192.Pin_1
  N61: R178.Pin_1, Second_Units.connector10
  N62: R179.Pin_1, Second_Units.connector9
  N63: R182.Pin_1, Second_Units.connector4
  N64: Second_Units.connector1, R180.Pin_1
  N65: Second_Units.connector2, R181.Pin_1
  N66: Second_Units.connector6, R183.Pin_1
  N67: Second_Units.connector7, R184.Pin_1

notes:
  +9V
  PCB-Fab by
  EQComponentes.com
  Design by
  Korama.es
  Designed using
  Fritzing.org
  Free Software
  +5V
  GND
  DATA
  LATCH
  CLK
  COLON
  CrossFit Chrono Viewer Digit PCB
  Rev 1.1 _ 06/APR/2015
