# Fritzing sketch id1236_Chrono_Controller_0 (saved by Fritzing 0.9.2b)
circuit board: 5.22876cm x 7.91581cm
breadboards: 1

parts:
  ATMEGA328P_PU = atmega328 [package=dip]
  C24 = Ceramic Capacitor [capacitance=100nF package="200 mil [THT, multilayer]"]
  C25 = Ceramic Capacitor [capacitance=100nF package="200 mil [THT, multilayer]"]
  J26 = female pin header, 6 pins [form="♀ (female)"]
  XTAL7 = Crystal [frequency="16 Mhz" package=THT]
  C26 = Ceramic Capacitor [capacitance=100nF package="200 mil [THT, multilayer]"]
  S6 = Pushbutton [package="[THT]"]
  C27 = Electrolytic Capacitor [capacitance=10µF package="100 mil [THT, electrolytic]"]
  C28 = Electrolytic Capacitor [capacitance=10µF package="100 mil [THT, electrolytic]"]
  C29 = Ceramic Capacitor [capacitance=22pF package="200 mil [THT, multilayer]"]
  C30 = Ceramic Capacitor [capacitance=22pF package="200 mil [THT, multilayer]"]
  R136 = Resistor [tolerance=±5% resistance=10k package=THT]
  D1 = Rectifier Diode [part_number=1N4007 package="300 mil [THT]"]
  R176 = Resistor [tolerance=±5% resistance=470 package=THT]
  J39 = screw terminal, 3 pins
  Q16 = NPN-Transistor [part_number=PN2222A package="TO92 [THT]"]
  K17 = Relay [part_number=FRS1B-S package=THT]
  LED10 = LED - 5mm [color="Red (633nm)" package="5 mm [THT]"]
  Power_plug1 = Power plug
  R177 = Resistor [tolerance=±5% resistance=220 package=THT]
  LED12 = LED - 5mm [color="Yellow (592nm)" package="5 mm [THT]"]
  R179 = Resistor [tolerance=±5% resistance=220 package=THT]
  LM7805 = Voltage Regulator - 5V [part_number=7805 package="TO220 [THT]"]
  J27 = screw terminal, 2 pins
  J42 = screw terminal, 2 pins
  J41 = screw terminal, 4 pins
  J43 = female pin header, 7 pins [form="♀ (female)"]
  S7 = Pushbutton [package="[THT]"]
  S8 = Pushbutton [package="[THT]"]
  S9 = Pushbutton [package="[THT]"]
  C31 = Ceramic Capacitor [capacitance=100nF package="200 mil [THT, multilayer]"]
  D17 = Rectifier Diode [part_number=1N4148 breakdown_voltage=3.6V package="300 mil [THT]"]

nets:
  N1: ATMEGA328P_PU.RESET, S6.Pin_3, S6.Pin_4, R136.Pin_0, C31.0
  N2: ATMEGA328P_PU.D0_(RX), J26.pin4
  N3: ATMEGA328P_PU.D1_(TX), J26.pin5
  N4: ATMEGA328P_PU.D2, J27.pin1
  N5: ATMEGA328P_PU.D3_(PWM), R176.Pin_0, LED12.anode
  N6: ATMEGA328P_PU.D4, J42.pin2
  N7: ATMEGA328P_PU.VCC, ATMEGA328P_PU.AVCC, ATMEGA328P_PU.AREF, C24.1, C25.0, J26.pin3, C26.1, C27.+, R136.Pin_1, K17.COIL2, LED10.anode, LM7805.output_voltage, J43.pin7, D17.cathode
  GND: ATMEGA328P_PU.GND, C24.0, C25.1, J26.pin1, C26.0, S6.Pin_1, S6.Pin_2, C27.-, C28.-, C29.0, C30.0, Q16.E, Power_plug1.GND, R177.Pin_1, R179.Pin_0, LM7805.GND, J27.pin2, J42.pin1, J41.pin1, J43.pin4, S7.Pin_3, S7.Pin_4, S8.Pin_3, S8.Pin_4, S9.Pin_3, S9.Pin_4
  N8: ATMEGA328P_PU.XLAT1, XTAL7.pin_1, C29.1
  N9: ATMEGA328P_PU.XLAT2, XTAL7.pin_0, C30.1
  N10: ATMEGA328P_PU.D5_(PWM), J41.pin2, S9.Pin_1, S9.Pin_2
  N11: ATMEGA328P_PU.D6_(PWM), J41.pin3, S8.Pin_1, S8.Pin_2
  N12: ATMEGA328P_PU.D8, J41.pin4, S7.Pin_1, S7.Pin_2
  N13: ATMEGA328P_PU.D9_(PWM), J43.pin5
  N14: ATMEGA328P_PU.D10_(PWM), J43.pin6
  N15: ATMEGA328P_PU.D11_(PWM), J43.pin3
  N16: ATMEGA328P_PU.D12, J43.pin2
  N17: J26.pin6, C31.1
  N18: C28.+, D1.cathode, LM7805.input_voltage, J43.pin1
  N19: R176.Pin_1, Q16.B
  N20: J39.pin1, K17.B
  N21: J39.pin2, K17.C1, K17.C2
  N22: J39.pin3, K17.A
  N23: Q16.C, K17.COIL1, D17.anode
  N24: LED10.cathode, R177.Pin_0
  N25: LED12.cathode, R179.Pin_1

notes:
  Rev 1.1 _ 16/APR/2015
  CrosFit Controller
  1
  1.- +5V
  2.- CLK
  3.- LATCH
  4.- GND
  5.- DATA
  6.- N/A
  7.- +9V
