# Fritzing sketch id1237_Chrono_Small_Digit_0 (saved by Fritzing 0.9.2b)
circuit board: 13.5775cm x 5.57073cm
breadboards: 1

parts:
  U11 = 74HC595 [package="DIP16 [THT]"]
  U12 = 74HC595 [package="DIP16 [THT]"]
  R178 = Resistor [tolerance=±5% resistance=150 package=THT]
  R179 = Resistor [tolerance=±5% resistance=150 package=THT]
  R180 = Resistor [tolerance=±5% resistance=150 package=THT]
  R181 = Resistor [tolerance=±5% resistance=150 package=THT]
  R182 = Resistor [tolerance=±5% resistance=150 package=THT]
  R183 = Resistor [tolerance=±5% resistance=150 package=THT]
  R184 = Resistor [tolerance=±5% resistance=150 package=THT]
  R185 = Resistor [tolerance=±5% resistance=150 package=THT]
  R186 = Resistor [tolerance=±5% resistance=150 package=THT]
  R187 = Resistor [tolerance=±5% resistance=150 package=THT]
  R188 = Resistor [tolerance=±5% resistance=150 package=THT]
  R189 = Resistor [tolerance=±5% resistance=150 package=THT]
  R190 = Resistor [tolerance=±5% resistance=150 package=THT]
  R191 = Resistor [tolerance=±5% resistance=150 package=THT]
  U13 = 74HC595 [package="DIP16 [THT]"]
  U14 = 74HC595 [package="DIP16 [THT]"]
  R192 = Resistor [tolerance=±5% resistance=150 package=THT]
  R193 = Resistor [tolerance=±5% resistance=150 package=THT]
  R194 = Resistor [tolerance=±5% resistance=150 package=THT]
  R195 = Resistor [tolerance=±5% resistance=150 package=THT]
  R196 = Resistor [tolerance=±5% resistance=150 package=THT]
  R197 = Resistor [tolerance=±5% resistance=150 package=THT]
  R198 = Resistor [tolerance=±5% resistance=150 package=THT]
  R199 = Resistor [tolerance=±5% resistance=150 package=THT]
  R200 = Resistor [tolerance=±5% resistance=150 package=THT]
  R201 = Resistor [tolerance=±5% resistance=150 package=THT]
  R202 = Resistor [tolerance=±5% resistance=150 package=THT]
  R203 = Resistor [tolerance=±5% resistance=150 package=THT]
  R204 = Resistor [tolerance=±5% resistance=150 package=THT]
  R205 = Resistor [tolerance=±5% resistance=150 package=THT]
  7_Segment6 = 7 Segment Display
  7_Segment7 = 7 Segment Display
  7_Segment8 = 7 Segment Display
  7_Segment9 = 7 Segment Display
  J1 = female pin header, 5 pins [form="♀ (female)"]

nets:
  N1: U11.Q1, R178.Pin_0
  N2: U11.Q2, R180.Pin_0
  N3: U11.Q3, R181.Pin_0
  N4: U11.Q4, R182.Pin_0
  N5: U11.Q5, R183.Pin_0
  N6: U11.Q6, R184.Pin_0
  GND: U11.GND, U11.OE, U12.GND, U12.OE, U13.GND, U13.OE, U14.GND, U14.OE, J1.pin2
  N7: U11.Q7', U12.DS
  VCC: U11.MR, U11.VCC, U12.MR, U12.VCC, U13.MR, U13.VCC, U14.MR, U14.VCC, 7_Segment6.common_anode, 7_Segment7.common_anode, 7_Segment8.common_anode, 7_Segment9.common_anode, J1.pin5
  N8: U11.SH_CP, U12.SH_CP, U13.SH_CP, U14.SH_CP, J1.pin4
  N9: U11.ST_CP, U12.ST_CP, U13.ST_CP, U14.ST_CP, J1.pin3
  N10: U11.DS, J1.pin1
  N11: U11.Q0, R179.Pin_0
  N12: U12.Q1, R186.Pin_0
  N13: U12.Q2, R190.Pin_0
  N14: U12.Q3, R188.Pin_0
  N15: U12.Q4, R189.Pin_0
  N16: U12.Q5, R185.Pin_0
  N17: U12.Q6, R187.Pin_0
  N18: U12.Q7', U14.DS
  N19: U12.Q0, R191.Pin_0
  N20: R178.Pin_1, 7_Segment6.Segment_B
  N21: R179.Pin_1, 7_Segment6.Segment_A
  N22: R180.Pin_1, 7_Segment6.Segment_C
  N23: R181.Pin_1, 7_Segment6.Segment_D
  N24: R182.Pin_1, 7_Segment6.Segment_E
  N25: R183.Pin_1, 7_Segment6.Segment_F
  N26: R184.Pin_1, 7_Segment6.Segment_G
  N27: R185.Pin_1, 7_Segment8.Segment_F
  N28: R186.Pin_1, 7_Segment8.Segment_B
  N29: R187.Pin_1, 7_Segment8.Segment_G
  N30: R188.Pin_1, 7_Segment8.Segment_D
  N31: R189.Pin_1, 7_Segment8.Segment_E
  N32: R190.Pin_1, 7_Segment8.Segment_C
  N33: R191.Pin_1, 7_Segment8.Segment_A
  N34: U13.Q1, R201.Pin_0
  N35: U13.Q2, R205.Pin_1
  N36: U13.Q3, R204.Pin_0
  N37: U13.Q4, R203.Pin_1
  N38: U13.Q5, R202.Pin_1
  N39: U13.Q6, R199.Pin_1
  N40: U13.DS, U14.Q7'
  N41: U13.Q0, R200.Pin_1
  N42: U14.Q1, R193.Pin_1
  N43: U14.Q2, R198.Pin_1
  N44: U14.Q3, R197.Pin_1
  N45: U14.Q4, R196.Pin_1
  N46: U14.Q5, R195.Pin_1
  N47: U14.Q6, R194.Pin_1
  N48: U14.Q0, R192.Pin_1
  N49: R192.Pin_0, 7_Segment7.Segment_A
  N50: R193.Pin_0, 7_Segment7.Segment_B
  N51: R194.Pin_0, 7_Segment7.Segment_G
  N52: R195.Pin_0, 7_Segment7.Segment_F
  N53: R196.Pin_0, 7_Segment7.Segment_E
  N54: R197.Pin_0, 7_Segment7.Segment_D
  N55: R198.Pin_0, 7_Segment7.Segment_C
  N56: R199.Pin_0, 7_Segment9.Segment_G
  N57: R200.Pin_0, 7_Segment9.Segment_A
  N58: R201.Pin_1, 7_Segment9.Segment_B
  N59: R202.Pin_0, 7_Segment9.Segment_F
  N60: R203.Pin_0, 7_Segment9.Segment_E
  N61: R204.Pin_1, 7_Segment9.Segment_D
  N62: R205.Pin_0, 7_Segment9.Segment_C

notes:
  Fritzing.org
  1-+5V
  4-GND
  5-DATA
  3-LATCH
  2-CLK
  CrossFit Chrono Viewer Digit PCB
  Rev 1.1 _ 06/APR/2015
  1
