# Fritzing sketch id1238_SmallBits_0 (saved by Fritzing 0.8.7b)
breadboards: 1

parts:
  7_Segment1 = 7 Segment Display
  S2 = Pushbutton [package="[THT]"]
  S3 = Pushbutton [package="[THT]"]
  VCC1 = Battery
  IC1 = IC, DIP package, 16 pins [chip_label=AND]
  IC2 = IC, DIP package, 16 pins [chip_label=NOT]

nets:
  N1: 7_Segment1.Segment_G, 7_Segment1.Segment_F, 7_Segment1.Segment_E, 7_Segment1.Segment_D, 7_Segment1.Segment_C, 7_Segment1.Segment_B, 7_Segment1.Segment_A, IC1.pin2, IC1.pin3, IC1.pin6, IC1.pin7
  N2: 7_Segment1.common_anode, S2.Pin_3, S2.Pin_4, S3.Pin_3, S3.Pin_4, VCC1.+, IC1.pin12, IC1.pin13, IC2.pin16
  N3: S2.Pin_1, S2.Pin_2, IC1.pin1, IC1.pin15, IC2.pin3, IC2.pin15
  N4: S3.Pin_1, S3.Pin_2, IC1.pin8, IC1.pin16, IC2.pin1, IC2.pin13
  N5: VCC1.-, IC1.pin4, IC1.pin5, IC2.pin8
  N6: IC1.pin9, IC2.pin12
  N7: IC1.pin10, IC2.pin4
  N8: IC1.pin11, IC2.pin2
  N9: IC1.pin14, IC2.pin14
