# Fritzing sketch id123_ultrasonido_medir_distancia_03_leds__0 (saved by Fritzing 0.9.3b)
breadboards: 1

parts:
  Parte1 = Arduino Uno (Rev3)
  R4 = Resistor [tolerance=±5% resistance=220 package=THT]
  LED16 = LED - 5mm [color="Red (633nm)" package="5 mm [THT]"]
  Parte2 = HC-SR04 ultrasonic distance sensor
  R7 = Resistor [tolerance=±5% resistance=220 package=THT]
  LED17 = LED - 5mm [color="Yellow (592nm)" package="5 mm [THT]"]
  R8 = Resistor [tolerance=±5% resistance=220 package=THT]
  LED18 = LED - 5mm [color="Green (565nm)" package="5 mm [THT]"]

nets:
  N1: Parte1.D11_PWM/MOSI, R4.Pin_0
  N2: Parte1.D12/MISO, R7.Pin_0
  N3: Parte1.D13/SCK, R8.Pin_0
  N4: Parte1.D5_PWM, Parte2.connector2
  N5: Parte1.D6_PWM, Parte2.connector1
  N6: Parte1.5V, Parte2.connector0
  N7: Parte1.GND, LED16.cathode, Parte2.connector3, LED17.cathode, LED18.cathode
  N8: R4.Pin_1, LED16.anode
  N9: R7.Pin_1, LED17.anode
  N10: R8.Pin_1, LED18.anode
