# Fritzing sketch id1240_CPR_3_LED_0 (saved by Fritzing 0.9.3b)
breadboards: 1

parts:
  J1 = Basic Force Sensing Resistor (FSR) [package=THT]
  Part1 = Arduino Uno (Rev3)
  R1 = Resistor [tolerance=±5% resistance=10 package=THT]
  LED1 = LED - 5mm [color="Red (633nm)" package="5 mm [THT]"]
  LED2 = LED - 5mm [color="Red (633nm)" package="5 mm [THT]"]
  LED3 = LED - 5mm [color="Red (633nm)" package="5 mm [THT]"]
  R2 = Resistor [tolerance=±5% resistance=220 package=THT]
  SPKR1 = Loudspeaker

nets:
  N1: J1.pin_0, Part1.A0, R1.Pin_1
  N2: J1.pin_1, Part1.5V
  N3: Part1.D9_PWM, R2.Pin_1
  N4: Part1.D11_PWM/MOSI, LED1.anode
  N5: Part1.D12/MISO, LED2.anode
  N6: Part1.D13/SCK, LED3.anode
  N7: Part1.GND, R1.Pin_0, LED1.cathode, LED2.cathode, LED3.cathode, SPKR1.pin1
  N8: R2.Pin_0, SPKR1.pin2
