# Fritzing sketch id1242_FRAM+ARDUINO_ADK_0 (saved by Fritzing 0.8.7b)
breadboards: 1

parts:
  Part1 = Arduino Mega ADK (Rev3)
  IC1 = IC, DIP package, 8 pins [chip_label=FRAM]

nets:
  N1: Part1.D21/SCL, IC1.pin6
  N2: Part1.D20/SDA, IC1.pin5
  N3: Part1.5V, IC1.pin8
  N4: Part1.GND, IC1.pin4
