# Fritzing sketch id1243_wiring_0 (saved by Fritzing 0.8.7b)

parts:
  IC1 = create_back [chip_label=50]
  SENSOR2 = TCS34725

nets:
  N1: IC1.connector20, SENSOR2.connector1
  N2: IC1.connector26, SENSOR2.connector3
  N3: IC1.connector28, SENSOR2.connector4
  N4: IC1.connector44, SENSOR2.connector6
  N5: IC1.connector48, SENSOR2.connector7
