# Fritzing sketch id1244_CribCandle_0 (saved by Fritzing 0.7.10b)
breadboards: 1

parts:
  Arduino1 = Arduino
  LED1 = LED - 5mm [color="Yellow (595nm)" package="5 mm [THT]"]
  LED2 = LED - 5mm [color="Red (633nm)" package="5 mm [THT]"]
  LED3 = LED - 5mm [color="Yellow (595nm)" package="5 mm [THT]"]
  R1 = Resistor [tolerance=±5% resistance=220 package=THT]
  R2 = Resistor [tolerance=±5% resistance=220 package=THT]
  R3 = Resistor [tolerance=±5% resistance=220 package=THT]
  VCC1 = 4 x AAA Battery Mount

nets:
  N1: Arduino1.GND, LED1.cathode, LED2.cathode, LED3.cathode, VCC1.-
  N2: Arduino1.D11, R1.Pin_1
  N3: Arduino1.D10, R2.Pin_1
  N4: Arduino1.D9, R3.Pin_1
  N5: Arduino1.+5V, VCC1.+
  N6: LED1.anode, R1.Pin_0
  N7: LED2.anode, R2.Pin_0
  N8: LED3.anode, R3.Pin_0

notes:
  CribCandle
  version 0.1 October 18, 2012
  Author : Michel Baily
  Try to simulate random lighting of a wood fire for Christmas Crib illumination
  For that purpose, we use 3 LEDs (2 Yellow, 1 Red) blinking randomly
