# Fritzing sketch id1245_criket_0 (saved by Fritzing 0.8.5b)
stripboards: 1

parts:
  atmega329 = atmega328 [package=dip]
  J5 = rounded female pin header, 3 pins [form="♀ (female rounded)"]
  BAT1 = Battery Holders [package=battery-aa-kit]
  Part1 = Arduino Uno (Rev3)
  J6 = Piezo Speaker
  J4 = female pin header, 4 pins [form="♀ (female)"]
  Part2 = Real Time Clock Module - DS1307 RTC Breakout Board
  J8 = female pin header, 2 pins [form="♀ (female)"]
  J9 = female pin header, 2 pins [form="♀ (female)"]

nets:
  N1: atmega329.RESET, J5.pin1, Part1.N/C
  N2: atmega329.D0_(RX), J5.pin2, Part1.D0/RX
  N3: atmega329.D1_(TX), J5.pin3, Part1.D1/TX
  N4: atmega329.D11_(PWM), J6.pin2, J8.pin2
  N5: atmega329.AVCC, BAT1.-, Part1.5V, J9.pin1
  N6: atmega329.GND#21, BAT1.+, Part1.GND, J6.pin1, J8.pin1, J9.pin2
  N7: atmega329.A4, Part2.SDA
  N8: J4.pin1, Part2.SCL
  N9: J4.pin3, Part2.5V
  N10: J4.pin4, Part2.GND
