# Fritzing sketch id1248_cronicasdenatal_0 (saved by Fritzing 0.9.3b)
breadboards: 1

parts:
  Componente1 = Arduino Uno (Rev3)
  J1 = Piezo Speaker
  Componente3 = Bluetooth HC-05 Macho
  R1 = Resistor [tolerance=±5% resistance=220 package="0402 [SMD]"]

nets:
  N1: Componente1.D9_PWM, R1.Pin_1
  N2: Componente1.D0/RX, Componente3.TXD
  N3: Componente1.D1/TX, Componente3.RXD
  5V: Componente1.5V, Componente3.VCC
  GND: Componente1.GND, J1.pin1, Componente3.GND
  N4: J1.pin2, R1.Pin_0
