# Fritzing sketch id1249_Arduino_Display (saved by Fritzing 0.3.19b)
breadboards: 1

parts:
  Arduino1 = Arduino
  R1 = Resistor [resistance=220 package=THT]
  LCD1 = LCD screen

nets:
  GND: Arduino1.GND, R1.Pin_0, R1.Pin_1, LCD1.VSS, LCD1.V0, LCD1.LED-
  N1: Arduino1.D13, LCD1.LED+
  N2: Arduino1.D12, LCD1.RS
  N3: Arduino1.D11, LCD1.R/W
  N4: Arduino1.D10, LCD1.E
  N5: Arduino1.D5, LCD1.DB4
  N6: Arduino1.D4, LCD1.DB5
  N7: Arduino1.D3, LCD1.DB6
  N8: Arduino1.D2, LCD1.DB7
  +5V: Arduino1.+5V, LCD1.VDD
