# Fritzing sketch id124_fan_0 (saved by Fritzing 0.9.2b)
circuit board: 8.46667cm x 5.64444cm
breadboards: 1

parts:
  Part1 = Arduino Uno (Rev3)
  LCD1 = LCD screen
  for_backlight = Resistor [tolerance=±5% resistance=220 package=THT]
  for_contrast = Trimmer Potentiometer [maximum_resistance=10kΩ package=THT]
  LM35_sensor = LM35 Temperature Sensor [package="TO92 [THT]"]
  4-pin_PWM_fan = Header 4 [package=screwterminal-3.5mm-4_lock]

nets:
  N1: Part1.A1, LM35_sensor.Vout
  N2: Part1.D8, 4-pin_PWM_fan.1
  N3: Part1.D9_PWM, 4-pin_PWM_fan.2
  N4: Part1.D11_PWM/MOSI, LCD1.E
  N5: Part1.D12/MISO, LCD1.RS
  GND: Part1.GND, LCD1.VSS, LCD1.R/W, for_contrast.leg2, LM35_sensor.GND, 4-pin_PWM_fan.4
  N6: Part1.D2, LCD1.DB7
  N7: Part1.D3_PWM, LCD1.DB6
  N8: Part1.D4, LCD1.DB5
  N9: Part1.D5_PWM, LCD1.DB4
  5V: Part1.5V, LCD1.VDD, for_backlight.Pin_0, for_contrast.leg1, LM35_sensor.+Vs, 4-pin_PWM_fan.3
  N10: LCD1.V0, for_contrast.wiper
