# Fritzing sketch id125_Relay_Timer_Reset_0 (saved by Fritzing 0.9.3b)

parts:
  Arduino1 = Arduino Uno (Rev3)
  WeMos_D1_Mini_Relay_Shield_V1 = WeMos D1 Mini Relay Shield V2  # not connected
  WeMos_D1_Mini_Relay_Shield_V2 = WeMos D1 Mini Relay Shield V2  # not connected
  WeMos_D1_Mini_Relay_Shield_V3 = WeMos D1 Mini Relay Shield V2  # not connected
  WeMos_D1_Mini_Relay_Shield_V4 = WeMos D1 Mini Relay Shield V2  # not connected
  S1 = Momentary Switch [package=ksa_sealed_tac_switch]
  S2 = Momentary Switch [package=ksa_sealed_tac_switch]
  S3 = Momentary Switch [package=ksa_sealed_tac_switch]
  S4 = Momentary Switch [package=ksa_sealed_tac_switch]
  S5 = Momentary Switch [package=ksa_sealed_tac_switch]
  LED1 = smd LED [color="Blue (525nm)" package="1206 [SMD]"]
  LED2 = smd LED [color="Green (570nm)" package="1206 [SMD]"]  # not connected
  LED3 = smd LED [color="Red (633nm)" package="1206 [SMD]"]  # not connected
  R1 = Resistor [tolerance=±5% resistance=1k package="0805 [SMD]"]
  R2 = Resistor [tolerance=±5% resistance=1k package="0805 [SMD]"]
  R3 = Resistor [tolerance=±5% resistance=1k package="0805 [SMD]"]  # not connected
  R4 = Resistor [tolerance=±5% resistance=1k package="0805 [SMD]"]
  R5 = Resistor [tolerance=±5% resistance=1k package="0805 [SMD]"]  # not connected
  R6 = Resistor [tolerance=±5% resistance=220 package="0805 [SMD]"]
  R7 = Resistor [tolerance=±5% resistance=220 package="0805 [SMD]"]
  R8 = Resistor [tolerance=±5% resistance=220 package="0805 [SMD]"]
  J1 = Power Jack [package=power_jack_combo]  # not connected

nets:
  N1: Arduino1.A0, S2.1
  N2: Arduino1.A1, S3.1
  N3: Arduino1.A2, S4.1
  N4: Arduino1.A3, S1.1
  N5: Arduino1.A4/SDA, S5.1
  N6: Arduino1.GND, LED1.cathode, R1.Pin_1, R2.Pin_1, R4.Pin_1
  N7: Arduino1.D3_PWM, R6.Pin_1
  N8: Arduino1.D5_PWM, R8.Pin_1
  N9: Arduino1.D6_PWM, R7.Pin_1

notes:
  BLINK
  RELAY1
  RELAY2
  RELAY3
  RELAY4
  BUTTON1
  BUTTON5
  BUTTON2
  BUTTON3
  BUTTON4
  timer reset
  4 RELAY MODULE
  5 x 1K
  3 x 220R
  5V
  GND
  Common GND
  External 5V
  JD-VCC
  GND  IN1  IN2  IN3  IN4  VCC
  4 RELAY SWITCH, 1 w/ TIMER
  soldering iron
