# Fritzing sketch id1262_Untitled_Sketch_4_0 (saved by Fritzing 0.9.2b)
breadboards: 1

parts:
  R1 = Resistor [tolerance=±5% resistance=220 package=THT]
  R2 = Resistor [tolerance=±5% resistance=220 package=THT]
  R3 = Resistor [tolerance=±5% resistance=220 package=THT]
  R4 = Resistor [tolerance=±5% resistance=220 package=THT]
  R5 = Resistor [tolerance=±5% resistance=220 package=THT]
  R6 = Resistor [tolerance=±5% resistance=220 package=THT]
  LED1 = LED - 5mm [color="Red (633nm)" package="5 mm [THT]"]
  LED2 = LED - 5mm [color="Red (633nm)" package="5 mm [THT]"]
  LED3 = LED - 5mm [color="Red (633nm)" package="5 mm [THT]"]
  LED4 = LED - 5mm [color="Red (633nm)" package="5 mm [THT]"]
  LED5 = LED - 5mm [color="Red (633nm)" package="5 mm [THT]"]
  LED6 = LED - 5mm [color="Red (633nm)" package="5 mm [THT]"]
  S1 = Pushbutton [package="[THT]"]
  R7 = Resistor [tolerance=±5% resistance=220 package=THT]
  Parte1 = Arduino Uno (Rev3)

nets:
  N1: R1.Pin_0, Parte1.D2
  N2: R1.Pin_1, LED1.anode
  N3: R2.Pin_0, Parte1.D4
  N4: R2.Pin_1, LED3.anode
  N5: R3.Pin_0, Parte1.D3_PWM
  N6: R3.Pin_1, LED2.anode
  N7: R4.Pin_0, Parte1.D5_PWM
  N8: R4.Pin_1, LED4.anode
  N9: R5.Pin_0, Parte1.D6_PWM
  N10: R5.Pin_1, LED5.anode
  N11: R6.Pin_0, Parte1.D7
  N12: R6.Pin_1, LED6.anode
  N13: LED1.cathode, LED2.cathode, LED3.cathode, LED4.cathode, LED5.cathode, LED6.cathode, S1.Pin_1, S1.Pin_2, R7.Pin_0, R7.Pin_1, Parte1.GND
  N14: S1.Pin_3, S1.Pin_4, Parte1.D8
