# Fritzing sketch id1264_circuito_en_paralelo_0 (saved by Fritzing 0.9.3b)
circuit board: 8.46667cm x 5.64444cm
breadboards: 1

parts:
  Componente1 = Arduino Uno (Rev3)
  R1 = Resistor [tolerance=±5% resistance=220 package=THT]  # not connected
  S1 = Pushbutton [package="[THT]"]
  S2 = Pushbutton [package="[THT]"]
  LED1 = LED - 5mm [color="Red (633nm)" package="5 mm [THT]"]

nets:
  N1: Componente1.GND, LED1.cathode
  N2: S1.Pin_1, S1.Pin_2, S2.Pin_1, S2.Pin_2, LED1.anode
  N3: S1.Pin_3, S1.Pin_4, S2.Pin_3, S2.Pin_4

notes:
  CIRCUITO EN PARALELO
