# Fritzing sketch id1265_CT_Coding_0 (saved by Fritzing 0.9.3b)

parts:
  Part1 = Arduino Uno (Rev3)
  J1 = Infrared Proximity Sensor
  LED1 = LED - 5mm [color="Red (633nm)" package="5 mm [THT]"]

nets:
  N1: Part1.A0, J1.Vout
  N2: Part1.D13/SCK, LED1.anode
  GND: Part1.GND, J1.GND, LED1.cathode
  5V: Part1.5V, J1.Vcc
