# Fritzing sketch id1266_PI_2_0 (saved by Fritzing 0.9.3b)
circuit board: 10cm x 16cm
breadboards: 2

parts:
  UTC7805 = Basic FET P-Channel [package="TO220 [THT]"]
  reset = Pushbutton [package="[THT]"]
  D1 = Rectifier Diode [part_number=1N4001 package="300 mil [THT]"]
  C6 = Electrolytic Capacitor [capacitance=10µF voltage=20V package="100 mil [THT, electrolytic]"]
  Re1 = Resistor [tolerance=±5% resistance=470 package=THT]
  C8 = Ceramic Capacitor [capacitance=10pF package="100 mil [THT, multilayer]"]
  LED = LED - 5mm [color="Green (555nm)" package="5 mm [THT]"]
  Cristal = Crystal [frequency="16 Mhz" package=THT]
  C7 = Ceramic Capacitor [capacitance=10pF voltage=6.3V package="100 mil [THT, multilayer]"]
  C3 = Electrolytic Capacitor [capacitance=22µF voltage=20V package="100 mil [THT, electrolytic]"]
  Q1 = TRANSISTOR_NPN [package=to-92]
  R1 = Resistor [tolerance=±1% resistance=220k package=THT]
  Q2 = TRANSISTOR_NPN [package=to-92]
  R2 = Resistor [tolerance=±1% resistance=220k package=THT]
  Q3 = TRANSISTOR_NPN [package=to-92]
  R3 = Resistor [tolerance=±1% resistance=220k package=THT]
  Q4 = TRANSISTOR_NPN [package=to-92]
  R4 = Resistor [tolerance=±1% resistance=220k package=THT]
  R15 = Resistor [tolerance=±1% resistance=470 package=THT]
  R14 = Resistor [tolerance=±1% resistance=470 package=THT]
  R13 = Resistor [tolerance=±1% resistance=470 package=THT]
  R16 = Resistor [tolerance=±1% resistance=470 package=THT]
  R12 = Resistor [tolerance=±1% resistance=470 package=THT]
  R11 = Resistor [tolerance=±1% resistance=470 package=THT]
  R10 = Resistor [tolerance=±1% resistance=470 package=THT]
  R9 = Resistor [tolerance=±1% resistance=470 package=THT]
  R7 = Resistor [tolerance=±1% resistance=470 package=THT]
  R2_2 = Resistor [tolerance=±2% resistance=470 package=THT]
  R3_2 = Resistor [tolerance=±1% resistance=470 package=THT]
  R1_2 = Resistor [tolerance=±1% resistance=470 package=THT]
  R8 = Resistor [tolerance=±1% resistance=470 package=THT]
  R6 = Resistor [tolerance=±1% resistance=470 package=THT]
  R5 = Resistor [tolerance=±1% resistance=470 package=THT]
  R4_2 = Resistor [tolerance=±1% resistance=470 package=THT]
  Re2 = Resistor [tolerance=±1% resistance=10k package=THT]
  Power_5-12v = Power plug
  Atmel_328p = atmega328 [package=dip]

nets:
  N1: UTC7805.gate, D1.cathode, C3.+
  GND: UTC7805.drain, reset.Pin_1, reset.Pin_2, C6.-, C8.1, LED.cathode, C7.0, C3.-, Q1.C, Q2.C, Q3.C, Q4.C, Power_5-12v.GND, Atmel_328p.GND
  N2: UTC7805.source, C6.+, Re1.Pin_1, Re2.Pin_0, Atmel_328p.VCC, Atmel_328p.AVCC, Atmel_328p.AREF
  N3: reset.Pin_3, reset.Pin_4, Re2.Pin_1, Atmel_328p.RESET
  N4: D1.anode, Power_5-12v.VCC
  N5: Re1.Pin_0, LED.anode
  N6: C8.0, Cristal.pin_0, Atmel_328p.XLAT1
  N7: Cristal.pin_1, C7.1, Atmel_328p.XLAT2
  N8: Q1.B, R1.Pin_0
  N9: R1.Pin_1, Atmel_328p.D5_(PWM)
  N10: Q2.B, R2.Pin_0
  N11: R2.Pin_1, Atmel_328p.D6_(PWM)
  N12: Q3.B, R3.Pin_0
  N13: R3.Pin_1, Atmel_328p.D7
  N14: Q4.B, R4.Pin_0
  N15: R4.Pin_1, Atmel_328p.D8
  N16: R15.Pin_1, Atmel_328p.D3_(PWM)
  N17: R14.Pin_1, Atmel_328p.D2
  N18: R13.Pin_1, Atmel_328p.D1_(TX)
  N19: R16.Pin_1, Atmel_328p.D4
  N20: R12.Pin_1, Atmel_328p.D0_(RX)
  N21: R11.Pin_1, Atmel_328p.A5
  N22: R10.Pin_1, Atmel_328p.A4
  N23: R9.Pin_1, Atmel_328p.A3
  N24: R7.Pin_1, Atmel_328p.A1
  N25: R2_2.Pin_1, Atmel_328p.D10_(PWM)
  N26: R3_2.Pin_1, Atmel_328p.D11_(PWM)
  N27: R1_2.Pin_1, Atmel_328p.D9_(PWM)
  N28: R8.Pin_1, Atmel_328p.A2
  N29: R6.Pin_1, Atmel_328p.A0
  N30: R5.Pin_1, Atmel_328p.D13
  N31: R4_2.Pin_1, Atmel_328p.D12

notes:
  Microcontrolador
  Fonte
  LED Fonte
  Projeto integrador 2017/1
  Leonardo Furini
  e
  Mateus Pardin
