# Fritzing sketch id1267_cube_0 (saved by Fritzing 0.9.2b)
circuit board: 8.46667cm x 5.64444cm
breadboards: 1

parts:
  Composant1 = Arduino Mega 2560 (Rev3)
  LED11 = RGB LED (com. cathode, rgb) [package="5 mm [THT]"]
  LED12 = RGB LED (com. cathode, rgb) [package="5 mm [THT]"]
  LED17 = RGB LED (com. cathode, rgb) [package="5 mm [THT]"]
  LED18 = RGB LED (com. cathode, rgb) [package="5 mm [THT]"]
  LED19 = RGB LED (com. cathode, rgb) [package="5 mm [THT]"]
  LED20 = RGB LED (com. cathode, rgb) [package="5 mm [THT]"]
  LED21 = RGB LED (com. cathode, rgb) [package="5 mm [THT]"]
  LED22 = RGB LED (com. cathode, rgb) [package="5 mm [THT]"]
  LED23 = RGB LED (com. cathode, rgb) [package="5 mm [THT]"]
  R1 = Resistor [tolerance=±5% resistance=110 package=THT]
  LED24 = RGB LED (com. cathode, rgb) [package="5 mm [THT]"]
  LED25 = RGB LED (com. cathode, rgb) [package="5 mm [THT]"]
  LED26 = RGB LED (com. cathode, rgb) [package="5 mm [THT]"]
  LED27 = RGB LED (com. cathode, rgb) [package="5 mm [THT]"]
  LED28 = RGB LED (com. cathode, rgb) [package="5 mm [THT]"]
  LED29 = RGB LED (com. cathode, rgb) [package="5 mm [THT]"]
  LED30 = RGB LED (com. cathode, rgb) [package="5 mm [THT]"]
  LED31 = RGB LED (com. cathode, rgb) [package="5 mm [THT]"]
  LED32 = RGB LED (com. cathode, rgb) [package="5 mm [THT]"]
  R2 = Resistor [tolerance=±5% resistance=110 package=THT]
  LED33 = RGB LED (com. cathode, rgb) [package="5 mm [THT]"]
  LED34 = RGB LED (com. cathode, rgb) [package="5 mm [THT]"]
  LED35 = RGB LED (com. cathode, rgb) [package="5 mm [THT]"]
  LED36 = RGB LED (com. cathode, rgb) [package="5 mm [THT]"]
  LED37 = RGB LED (com. cathode, rgb) [package="5 mm [THT]"]
  LED38 = RGB LED (com. cathode, rgb) [package="5 mm [THT]"]
  LED39 = RGB LED (com. cathode, rgb) [package="5 mm [THT]"]
  LED40 = RGB LED (com. cathode, rgb) [package="5 mm [THT]"]
  LED41 = RGB LED (com. cathode, rgb) [package="5 mm [THT]"]
  R3 = Resistor [tolerance=±5% resistance=110 package=THT]

nets:
  N1: Composant1.D5_PWM, R2.Pin_1
  N2: Composant1.D6_PWM, R1.Pin_1
  N3: Composant1.D7_PWM, R3.Pin_1
  N4: Composant1.D23, LED11.red_anode, LED24.red_anode, LED33.red_anode
  N5: Composant1.D24, LED11.blue_anode, LED24.blue_anode, LED33.blue_anode
  N6: Composant1.D25, LED11.green_anode, LED24.green_anode, LED33.green_anode
  N7: Composant1.D26, LED12.red_anode, LED31.red_anode, LED40.red_anode
  N8: Composant1.D27, LED12.blue_anode, LED31.blue_anode, LED40.blue_anode
  N9: Composant1.D28, LED12.green_anode, LED31.green_anode, LED40.green_anode
  N10: Composant1.D29, LED17.red_anode, LED27.red_anode, LED36.red_anode
  N11: Composant1.D30, LED17.blue_anode, LED27.blue_anode, LED36.blue_anode
  N12: Composant1.D31, LED17.green_anode, LED27.green_anode, LED36.green_anode
  N13: Composant1.D32, LED20.red_anode, LED30.red_anode, LED39.red_anode
  N14: Composant1.D33, LED20.blue_anode, LED30.blue_anode, LED39.blue_anode
  N15: Composant1.D34, LED20.green_anode, LED30.green_anode, LED39.green_anode
  N16: Composant1.D35, LED19.red_anode, LED28.red_anode, LED37.red_anode
  N17: Composant1.D36, LED19.blue_anode, LED28.blue_anode, LED37.blue_anode
  N18: Composant1.D37, LED19.green_anode, LED28.green_anode, LED37.green_anode
  N19: Composant1.D38, LED18.red_anode, LED32.red_anode, LED41.red_anode
  N20: Composant1.D39, LED18.blue_anode, LED32.blue_anode, LED41.blue_anode
  N21: Composant1.D40, LED18.green_anode, LED32.green_anode, LED41.green_anode
  N22: Composant1.D41, LED23.red_anode, LED29.red_anode, LED38.red_anode
  N23: Composant1.D42, LED23.blue_anode, LED29.blue_anode, LED38.blue_anode
  N24: Composant1.D43, LED23.green_anode, LED29.green_anode, LED38.green_anode
  N25: Composant1.D44, LED21.red_anode, LED26.red_anode, LED35.red_anode
  N26: Composant1.D45, LED21.blue_anode, LED26.blue_anode, LED35.blue_anode
  N27: Composant1.D46, LED21.green_anode, LED26.green_anode, LED35.green_anode
  N28: Composant1.D47, LED22.red_anode, LED25.red_anode, LED34.red_anode
  N29: Composant1.D48, LED22.blue_anode, LED25.blue_anode, LED34.blue_anode
  N30: Composant1.D49, LED22.green_anode, LED25.green_anode, LED34.green_anode
  N31: LED11.common_cathode, LED12.common_cathode, LED17.common_cathode, LED18.common_cathode, LED19.common_cathode, LED20.common_cathode, LED21.common_cathode, LED22.common_cathode, LED23.common_cathode, R1.Pin_0
  N32: LED24.common_cathode, LED25.common_cathode, LED26.common_cathode, LED27.common_cathode, LED28.common_cathode, LED29.common_cathode, LED30.common_cathode, LED31.common_cathode, LED32.common_cathode, R2.Pin_0
  N33: LED33.common_cathode, LED34.common_cathode, LED35.common_cathode, LED36.common_cathode, LED37.common_cathode, LED38.common_cathode, LED39.common_cathode, LED40.common_cathode, LED41.common_cathode, R3.Pin_0
