# Fritzing sketch id1269_2DMiller_0 (saved by Fritzing 0.9.1b)
circuit board: 7.5cm x 5.6cm
breadboards: 1
perfboards: 1

parts:
  Main_Controller = atmega168 [package=dip]
  ASP = shrouded pin header, 10 pins [form="♂ (shrouded male)"]
  NEMA_17_Motor_2 = Stepper Motor - Bipolar
  VREG = Voltage Regulator - 3.3V [package="TO220 [THT]"]
  Bit_Motor = DC Motor
  Stepper_Driver_1 = EasyDriver_v44
  Stepper_Driver_2 = EasyDriver_v44
  NEMA_17_Motor_1 = Stepper Motor - Bipolar
  TTL_Header = male pin header, 3 pins [form="♂ (male)"]

nets:
  N1: Main_Controller.RESET, ASP.pin3, Stepper_Driver_1.RESET, Stepper_Driver_2.RESET
  N2: Main_Controller.D0_(RX), Stepper_Driver_1.STEP
  N3: Main_Controller.D1_(TX), Stepper_Driver_2.STEP
  N4: Main_Controller.D2, Bit_Motor.pin_1
  N5: Main_Controller.D3_(PWM), Stepper_Driver_1.DIR
  N6: Main_Controller.D4, Stepper_Driver_2.DIR
  VCC: Main_Controller.VCC, Main_Controller.AVCC, Main_Controller.AREF, ASP.pin10, VREG.output_voltage, Stepper_Driver_1.VCC, Stepper_Driver_1.SLEEP, Stepper_Driver_1.ENABLE, Stepper_Driver_2.VCC, Stepper_Driver_2.ENABLE
  GND: Main_Controller.GND, ASP.pin6, ASP.pin7, ASP.pin8, ASP.pin9, VREG.GND, Bit_Motor.pin_2, Stepper_Driver_1.GND, Stepper_Driver_2.GND, TTL_Header.pin3
  N7: Main_Controller.D10_(PWM), ASP.pin5
  N8: Main_Controller.D11_(PWM), ASP.pin1
  N9: Main_Controller.A0, TTL_Header.pin1
  N10: Main_Controller.A1, TTL_Header.pin2
  N11: NEMA_17_Motor_2.A, Stepper_Driver_2.OUT2A
  N12: NEMA_17_Motor_2.C, Stepper_Driver_2.OUT2B
  N13: NEMA_17_Motor_2.B, Stepper_Driver_2.OUT1B
  N14: NEMA_17_Motor_2.D, Stepper_Driver_2.OUT1A
  12V: VREG.input_voltage, Stepper_Driver_1.V+, Stepper_Driver_2.V+
  N15: Stepper_Driver_1.OUT2A, NEMA_17_Motor_1.A
  N16: Stepper_Driver_1.OUT2B, NEMA_17_Motor_1.C
  N17: Stepper_Driver_1.OUT1A, NEMA_17_Motor_1.D
  N18: Stepper_Driver_1.OUT1B, NEMA_17_Motor_1.B

notes:
  CullMill 0.1
