# Fritzing sketch id126_quadservo_0 (saved by Fritzing 0.9.3b)
breadboards: 1

parts:
  R1 = Rotary Potentiometer (Small) [maximum_resistance=100kΩ package=THT]
  R2 = Rotary Potentiometer (Small) [maximum_resistance=100kΩ package=THT]
  R3 = Rotary Potentiometer (Small) [maximum_resistance=100kΩ package=THT]
  R4 = Rotary Potentiometer (Small) [maximum_resistance=100kΩ package=THT]
  J1 = Basic Servo
  J2 = Basic Servo
  J3 = Basic Servo
  J4 = Basic Servo
  Part1 = Arduino Uno (Rev3)

nets:
  VCC: R1.leg1, R2.leg1, R3.leg1, R4.leg1, J1.vcc, J2.vcc, J3.vcc, J4.vcc, Part1.5V
  N1: R1.wiper, Part1.A1
  GND: R1.leg2, R2.leg2, R3.leg2, R4.leg2, J1.gnd, J2.gnd, J3.gnd, J4.gnd, Part1.GND
  N2: R2.wiper, Part1.A0
  N3: R3.wiper, Part1.A2
  N4: R4.wiper, Part1.A3
  N5: J1.pulse, Part1.D10_PWM/SS
  N6: J2.pulse, Part1.D9_PWM
  N7: J3.pulse, Part1.D8
  N8: J4.pulse, Part1.D11_PWM/MOSI
