# Fritzing sketch id1270_cooler_0 (saved by Fritzing 0.7.12b)
breadboards: 1

parts:
  Arduino1 = Arduino
  R1 = Resistor [tolerance=±5% resistance=220 package=THT]
  U1 = Optocoupler [package=THT]
  M1 = DC Motor
  T1 = LM35 Temperature Sensor [package="TO92 [THT]"]
  J1 = Peltier Element
  12v = Power plug

nets:
  N1: Arduino1.D9, R1.Pin_0
  N2: Arduino1.+5V, T1.+Vs
  GND: Arduino1.GND, U1.Pin_2, T1.GND
  N3: Arduino1.A0, T1.Vout
  N4: R1.Pin_1, U1.Pin_1
  N5: U1.Pin_4, M1.pin_1
  N6: U1.Pin_5, M1.pin_2, J1.pin1, 12v.GND
  N7: J1.pin2, 12v.VCC
