# Fritzing sketch id1271_Cupdraw_0 (saved by Fritzing 0.9.3b)
breadboards: 1

parts:
  LCD = LCD screen
  PB1 = Pushbutton [package="[THT]"]
  PB2 = Pushbutton [package="[THT]"]
  PB3 = Pushbutton [package="[THT]"]
  PB4 = Pushbutton [package="[THT]"]
  A11 = Basic Servo
  LS1 = Basic Servo
  A21 = Basic Servo
  A12 = Basic Servo
  S2 = Solenoid
  S1 = Solenoid
  A22 = Basic Servo
  LS2 = Basic Servo
  Pot = TRIMPOT [package=trimpot-3mm-2]
  Relay = RELAY [package=relay-t9a-2]
  U1 = RELAY [package=relay-t9a-2]
  U2 = RELAY [package=relay-t9a-2]
  Part4 = Arduino Mega ADK (Rev3)

nets:
  N1: LCD.VSS, Pot.CCW
  VCC: LCD.VDD, LS1.vcc, LS2.vcc, Pot.CW, U1.COIL2, U2.COIL2, Part4.5V
  N2: LCD.V0, Pot.WIPER
  N3: LCD.RS, Part4.D30
  N4: LCD.E, Part4.D31
  N5: LCD.DB3, Part4.D32
  N6: LCD.DB4, Part4.D33
  N7: LCD.DB5, Part4.D34
  N8: LCD.DB6, Part4.D35
  Gnd: PB1.Pin_1, PB1.Pin_2, PB2.Pin_1, PB2.Pin_2, PB3.Pin_1, PB3.Pin_2, PB4.Pin_1, PB4.Pin_2, LS1.gnd, LS2.gnd, Relay.NC, U1.COIL1, U2.COIL1, Part4.GND
  N9: PB1.Pin_3, PB1.Pin_4, Part4.D16/TX2
  N10: PB2.Pin_3, PB2.Pin_4, Part4.D17/RX2
  N11: PB3.Pin_3, PB3.Pin_4, Part4.D18/TX1
  N12: PB4.Pin_3, PB4.Pin_4, Part4.D21/SCL
  GND: A11.gnd, A21.gnd, A12.gnd, A22.gnd
  5V: A11.vcc, A21.vcc, A12.vcc, A22.vcc
  N13: A11.pulse, A12.pulse, Part4.D8_PWM
  N14: LS1.pulse, Part4.D6_PWM
  N15: A21.pulse, A22.pulse, Part4.D9_PWM
  N16: S2.pin1, U2.NO
  N17: S1.pin1, U1.NO
  N18: LS2.pulse, Part4.D7_PWM
  N19: Relay.NO, Part4.D48
  N20: U1.MAIN, U2.MAIN
  N21: U1.NC, Part4.D47
  N22: U2.NC, Part4.D46
  MISO: Part4.D50/MISO
  MOSI: Part4.D51/MOSI
  SCK: Part4.D52/SCK

notes:
  ACTUATOR_1
  ACTUATOR_2
  LEVELSERVO_1
  LEVESERVO_2
  These 2 wires technically get connected by water to act as a level sensor.
  LEVELSERVO_2
  Left Button
  Right Button
  OK/Start Button
  Menu Button
  120V input
  SD Shield
