# Fritzing sketch id1272_CUTSIE_WHUN_KICK_STANDS_0 (saved by Fritzing 0.9.3b)
breadboards: 1

parts:
  Part1 = Arduino Nano (Rev3.0)
  Part2 = Arduino Pro Mini (5V)
  Part3 = Triple Axis Accelerometer Breakout - ADXL335
  U1 = L9110 H-bridge [part_number="L9110 H-bridge"]
  M1 = DC Motor
  M2 = DC Motor
  J1 = Basic Servo
  J2 = Basic Servo

nets:
  GND: Part1.GND, Part2.GND, Part3.GND, U1.connector2, J1.gnd, J2.gnd
  N1: Part1.D5, U1.connector5
  N2: Part1.D7, U1.connector4
  N3: Part1.D9, U1.connector1
  N4: Part1.D11/MOSI, U1.connector0
  VCC: Part1.5V, Part2.VCC, Part3.VCC, U1.connector3, J1.vcc, J2.vcc
  N5: Part1.A5, Part2.A5
  N6: Part1.A4, Part2.A4
  N7: Part1.A3, Part2.A3
  N8: Part2.A2, Part3.ZOUT
  N9: Part2.A1, Part3.YOUT
  N10: Part2.A0, Part3.XOUT
  N11: U1.connector6, M1.pin_2
  N12: U1.connector7, M1.pin_1
  N13: U1.connector8, M2.pin_2
  N14: U1.connector9, M2.pin_1
  N15: J1.pulse, J2.pulse

notes:
  Right Side motor and
  rear Jackstands
  Left Side motor and
  front Jackstands
