# Fritzing sketch id1273_CUTSIE_WHUN_0 (saved by Fritzing 0.9.3b)
breadboards: 2

parts:
  hc-sr1 = hc-sr04
  U2 = L9110 H-bridge [part_number="L9110 H-bridge"]
  Arduino1 = Arduino Mini (Rev5)
  GY1 = MPU-6050 GY-521 [form="♀ (female)"]
  Power_plug1 = Power plug
  U3 = Voltage Regulator - 5V [package="DPak [SMD]"]
  C1 = Electrolytic Capacitor [capacitance=10nF package="100 mil [THT, electrolytic]"]
  C2 = Electrolytic Capacitor [capacitance=100nF package="100 mil [THT, electrolytic]"]
  S1 = Toggle Switch [package=THT]
  BAT1 = Battery Holders [package=lipo-1100mAh]
  BAT2 = Battery Holders [package=lipo-1100mAh]
  M1 = DC Motor
  M2 = DC Motor
  J1 = Piezo Speaker
  LED1 = LED - 5mm [color="Red (633nm)" package="5 mm [THT]"]
  R1 = Resistor [tolerance=±5% resistance=220 package=THT]
  JP1 = Header 12 [package=1x12_machine-pin-header_lock.004]

nets:
  VCC: hc-sr1.VCC, Arduino1.VCC, U3.output_voltage, C2.+, LED1.anode
  N1: hc-sr1.Trig, Arduino1.D3_PWM
  N2: hc-sr1.Echo, Arduino1.D4
  GND: hc-sr1.GND, U2.connector2, Arduino1.GND, GY1.connector1, Power_plug1.GND, U3.GND, C1.-, C2.-, BAT2.-, J1.pin1, R1.Pin_0, JP1.12
  N3: U2.connector0, Arduino1.D5_PWM
  N4: U2.connector1, Arduino1.D6_PWM
  N5: U2.connector3, S1.COM, BAT1.+
  N6: U2.connector4, Arduino1.D10_PWM
  N7: U2.connector5, Arduino1.D11_PWM
  N8: U2.connector6, M1.pin_1
  N9: U2.connector7, M1.pin_2
  N10: U2.connector8, M2.pin_1
  N11: U2.connector9, M2.pin_2
  N12: Arduino1.D2, GY1.connector7
  N13: Arduino1.D7, J1.pin2
  N14: Arduino1.D8, JP1.4
  N15: Arduino1.D9_PWM, JP1.3
  N16: Arduino1.5V, GY1.connector0, JP1.11
  N17: Arduino1.A3, JP1.8
  N18: Arduino1.A2, JP1.7
  N19: Arduino1.A1, JP1.6
  N20: Arduino1.A0, JP1.5
  N21: Arduino1.A4, GY1.connector3
  N22: Arduino1.A5, GY1.connector2
  N23: Power_plug1.VCC, S1.L2
  N24: U3.input_voltage, C1.+, S1.L1
  N25: BAT1.-, BAT2.+
  N26: LED1.cathode, R1.Pin_1

notes:
  Items in this area are installed into the upper portion of the robot (The Head)
  On/Off/Charge switch is located on back of head.
  Sonic distance sensors are also in the head.
  RC Receiver:
  wire color - use
  black - Ground
  Red - 5v Power
  Blue - CH1
  Yellow - CH2
  Green - CH3
  Grey - CH4
  White - CH5
  Orange - CH6
