# Fritzing sketch id1274_KronisV4_0 (saved by Fritzing 0.9.3b)
breadboards: 2

parts:
  Part1 = Bluetooth HC-05 Macho
  M2 = DC Motor
  hc-sr1 = hc-sr04
  RHT1 = Humidity and Temperature Sensor RHT03
  S1 = Ponte-H L298N
  M3 = DC Motor
  VCC1 = Battery block 9V
  VCC2 = Battery block 9V  # not connected
  R1 = Resistor [tolerance=±5% resistance=220 package=THT]
  J1 = Piezo Speaker
  LED1 = LED - 3mm [color="Red (633nm)" package="3 mm [THT]"]
  R2 = Resistor [tolerance=±5% resistance=220 package=THT]
  Part3 = Arduino Mega 2560 (Rev3)
  Nokia_5110_LCD_Module1 = Nokia 5110 LCD (8 pin)

nets:
  N1: Part1.TXD, Part3.D1_TX0
  N2: Part1.RXD, Part3.D0_RX0
  VCC: Part1.VCC, Part3.3V3, Nokia_5110_LCD_Module1.connector1, Nokia_5110_LCD_Module1.connector3
  GND: Part1.GND, Part3.GND, Nokia_5110_LCD_Module1.connector2
  N3: M2.pin_1, S1.connector10
  N4: M2.pin_2, S1.connector11
  VCC_2: hc-sr1.VCC, RHT1.Vcc, Part3.5V
  N5: hc-sr1.Trig, Part3.D12_PWM
  N6: hc-sr1.Echo, Part3.D13_PWM
  N7: hc-sr1.GND, RHT1.GND_2, S1.connector2, VCC1.-, J1.pin1
  N8: S1.connector1, VCC1.+
  N9: S1.connector4, Part3.D3_PWM
  N10: S1.connector5, Part3.D2_PWM
  N11: S1.connector7, Part3.D6_PWM
  N12: S1.connector8, Part3.D7_PWM
  N13: S1.connector9, Part3.D5_PWM
  N14: S1.connector13, M3.pin_2
  N15: S1.connector14, M3.pin_1
  N16: R1.Pin_1, Part3.D11_PWM
  N17: J1.pin2, Part3.D10_PWM
  N18: LED1.cathode, R2.Pin_0
  N19: R2.Pin_1, Part3.D9_PWM
  N20: Part3.D22, Nokia_5110_LCD_Module1.connector4
  N21: Part3.D23, Nokia_5110_LCD_Module1.connector5
  N22: Part3.D24, Nokia_5110_LCD_Module1.connector6
  N23: Part3.D25, Nokia_5110_LCD_Module1.connector0
  N24: Part3.D26, Nokia_5110_LCD_Module1.connector7
