# Fritzing sketch id1275_cycleleds_0 (saved by Fritzing 0.9.2b)
breadboards: 1

parts:
  Componente1 = Arduino Uno (Rev3)
  LED1 = LED - 5mm [color="Red (633nm)" package="5 mm [THT]"]
  R1 = Resistor [tolerance=±5% resistance=250 package=THT]
  R2 = Resistor [tolerance=±5% resistance=250 package=THT]
  R3 = Resistor [tolerance=±5% resistance=250 package=THT]
  R4 = Resistor [tolerance=±5% resistance=250 package=THT]
  R5 = Resistor [tolerance=±5% resistance=250 package=THT]
  LED2 = LED - 5mm [color="Red (633nm)" package="5 mm [THT]"]
  LED3 = LED - 5mm [color="Red (633nm)" package="5 mm [THT]"]
  LED4 = LED - 5mm [color="Red (633nm)" package="5 mm [THT]"]
  LED5 = LED - 5mm [color="Red (633nm)" package="5 mm [THT]"]

nets:
  N1: Componente1.D9_PWM, R5.Pin_1
  N2: Componente1.D10_PWM/SS, R4.Pin_1
  N3: Componente1.D11_PWM/MOSI, R3.Pin_1
  N4: Componente1.D12/MISO, R2.Pin_1
  N5: Componente1.D13/SCK, R1.Pin_1
  N6: Componente1.GND, LED1.cathode, LED2.cathode, LED3.cathode, LED4.cathode, LED5.cathode
  N7: LED1.anode, R1.Pin_0
  N8: R2.Pin_0, LED2.anode
  N9: R3.Pin_0, LED3.anode
  N10: R4.Pin_0, LED4.anode
  N11: R5.Pin_0, LED5.anode
