# Fritzing sketch id1276_Rele8Registr_0 (saved by Fritzing 0.9.3b)
circuit board: 4.00792cm x 1.98291cm

parts:
  U1 = 74HC595 [package="DIP16 [THT]"]

nets:
  N1: U1.MR, U1.VCC

notes:
  VCC
  GND
  DS
  ST_CP
  SH_CP
  OE
  D15
  D14
  D13
  D12
  Q7'
  1
  2
  3
  4
  5
  6
  7
  8
