# Fritzing sketch id1277_Flip_Flop_from_Nand_0 (saved by Fritzing 0.9.3b)
breadboards: 1

parts:
  U1 = 74HC00
  U2 = CD4069UB
  S1 = Pushbutton [package="[THT]"]
  R1 = Resistor [tolerance=±5% resistance=10k package=THT]
  S2 = Toggle Switch [package=THT]

nets:
  N1: U1.connector0, U2.connector0, S2.COM
  N2: U1.connector1, U1.connector3, S1.Pin_1, S1.Pin_2, R1.Pin_0
  N3: U1.connector2, U1.connector12
  N4: U1.connector4, U2.connector1
  N5: U1.connector5, U1.connector8
  N6: U1.connector6, U2.connector6, R1.Pin_1, S2.L1
  N7: U1.connector7, U1.connector11
  N8: U1.connector9, U1.connector10
  N9: U1.connector13, U2.connector13, S1.Pin_3, S1.Pin_4
