# Fritzing sketch id1279_dado_electronico_0 (saved by Fritzing 0.9.3b)
breadboards: 1

parts:
  R1 = Resistor [tolerance=±5% resistance=220 package=THT]
  LED1 = LED - 5mm [color="Red (633nm)" package="5 mm [THT]"]
  LED2 = LED - 5mm [color="Red (633nm)" package="5 mm [THT]"]
  LED3 = LED - 5mm [color="Red (633nm)" package="5 mm [THT]"]
  LED4 = LED - 5mm [color="Red (633nm)" package="5 mm [THT]"]
  LED5 = LED - 5mm [color="Red (633nm)" package="5 mm [THT]"]
  LED6 = LED - 5mm [color="Red (633nm)" package="5 mm [THT]"]
  LED7 = LED - 5mm [color="Red (633nm)" package="5 mm [THT]"]
  R2 = Resistor [tolerance=±5% resistance=220 package=THT]
  R3 = Resistor [tolerance=±5% resistance=220 package=THT]
  R4 = Resistor [tolerance=±5% resistance=220 package=THT]
  R5 = Resistor [tolerance=±5% resistance=220 package=THT]
  R6 = Resistor [tolerance=±5% resistance=220 package=THT]
  R7 = Resistor [tolerance=±5% resistance=220 package=THT]
  Componente1 = Arduino Uno (Rev3)
  S1 = Pushbutton [package="[THT]"]
  R8 = Resistor [tolerance=±5% resistance=10k package=THT]

nets:
  N1: R1.Pin_0, LED2.anode
  N2: R1.Pin_1, Componente1.D3_PWM
  N3: LED1.cathode, LED2.cathode, LED3.cathode, LED4.cathode, LED5.cathode, LED6.cathode, LED7.cathode, Componente1.GND, R8.Pin_0
  N4: LED1.anode, R2.Pin_1
  N5: LED3.anode, R3.Pin_0
  N6: LED4.anode, R7.Pin_1
  N7: LED5.anode, R6.Pin_1
  N8: LED6.anode, R5.Pin_0
  N9: LED7.anode, R4.Pin_0
  N10: R2.Pin_0, Componente1.D2
  N11: R3.Pin_1, Componente1.D4
  N12: R4.Pin_1, Componente1.D5_PWM
  N13: R6.Pin_0, Componente1.D7
  N14: R7.Pin_0, Componente1.D6_PWM
  N15: Componente1.D10_PWM/SS, S1.Pin_3, S1.Pin_4, R8.Pin_1
  N16: Componente1.5V, S1.Pin_1, S1.Pin_2
