# Fritzing sketch id127_4017_proto_layout_0 (saved by Fritzing 0.9.0b)
perfboards: 1

parts:
  IC1 = IC, DIP package, 16 pins [chip_label=IC]  # not connected
  D3 = Rectifier Diode [part_number=1N914 package="300 mil [THT]"]  # not connected
  D6 = Rectifier Diode [part_number=1N914 package="300 mil [THT]"]  # not connected
  D7 = Rectifier Diode [part_number=1N914 package="300 mil [THT]"]  # not connected
  D8 = Rectifier Diode [part_number=1N914 package="300 mil [THT]"]  # not connected
  S1 = Toggle Switch [package=THT]
  VCC1 = Battery block 9V
  U1 = 3.5mm Audio Jack [package=audio-jack-3.5mm-smd]  # not connected
  R4 = Rotary Potentiometer (Large) [maximum_resistance=100kΩ package=THT]
  R6 = Rotary Potentiometer (Large) [maximum_resistance=100kΩ package=THT]
  R3 = Rotary Potentiometer (Large) [maximum_resistance=100kΩ package=THT]
  R5 = Rotary Potentiometer (Large) [maximum_resistance=100kΩ package=THT]
  U2 = 3.5mm Audio Jack [package=audio-jack-3.5mm-smd]  # not connected

nets:
  N1: S1.L1, VCC1.+
  N2: R4.leg1, R6.leg1, R3.leg1, R5.leg1

notes:
  jack: clock input
  jack: sequencer output
  X
