# Fritzing sketch id1280_dado_0 (saved by Fritzing 0.7.10b)
breadboards: 1

parts:
  7_Segment1 = 7-Segment LED Display [package=THT]
  R1 = Resistor [tolerance=±5% resistance=220 package=THT]
  R2 = Resistor [tolerance=±5% resistance=220 package=THT]
  R3 = Resistor [tolerance=±5% resistance=220 package=THT]
  R4 = Resistor [tolerance=±5% resistance=220 package=THT]
  R5 = Resistor [tolerance=±5% resistance=220 package=THT]
  R6 = Resistor [tolerance=±5% resistance=220 package=THT]
  R7 = Resistor [tolerance=±5% resistance=220 package=THT]
  S1 = Pushbutton [package="[THT]"]
  R8 = Resistor [tolerance=±5% resistance=3.9k package=THT]
  Arduino_Ethernet_Shield1 = Arduino Ethernet Shield
  Q1 = NPN-Transistor [package="TO92 [THT]"]
  R9 = Resistor [tolerance=±5% resistance=3.9k package=THT]

nets:
  N1: 7_Segment1.cathodeE, R3.Pin_1
  N2: 7_Segment1.cathodeD, R4.Pin_1
  N3: 7_Segment1.commAnode#2, Q1.C
  N4: 7_Segment1.cathodeC, R7.Pin_1
  N5: 7_Segment1.cathodeB, R6.Pin_1
  N6: 7_Segment1.cathodeA, R5.Pin_1
  N7: 7_Segment1.cathodeF, R2.Pin_1
  N8: 7_Segment1.cathodeG, R1.Pin_1
  N9: R1.Pin_0, Arduino_Ethernet_Shield1.D8
  N10: R2.Pin_0, Arduino_Ethernet_Shield1.D7
  N11: R3.Pin_0, Arduino_Ethernet_Shield1.D6
  N12: R4.Pin_0, Arduino_Ethernet_Shield1.D5
  N13: R5.Pin_0, Arduino_Ethernet_Shield1.D2
  N14: R6.Pin_0, Arduino_Ethernet_Shield1.D3
  N15: R7.Pin_0, Arduino_Ethernet_Shield1.SS#11
  N16: S1.Pin_1, S1.Pin_2, Arduino_Ethernet_Shield1.GND, Q1.E
  N17: S1.Pin_3, S1.Pin_4, R8.Pin_0, Arduino_Ethernet_Shield1.SS#5
  N18: R8.Pin_1, Arduino_Ethernet_Shield1.+5V
  N19: Arduino_Ethernet_Shield1.D9, R9.Pin_1
  N20: Q1.B, R9.Pin_0
