# Fritzing sketch id1281_dads_light_0 (saved by Fritzing 0.9.0b)
circuit board: 4.60021cm x 6.01134cm
breadboards: 1

parts:
  LED1 = LED - 5mm [color="Red (633nm)" package="5 mm [THT]"]
  LED2 = LED - 5mm [color="Red (633nm)" package="5 mm [THT]"]
  LED3 = LED - 5mm [color="Red (633nm)" package="5 mm [THT]"]
  LED4 = LED - 5mm [color="Red (633nm)" package="5 mm [THT]"]
  LED5 = LED - 5mm [color="Red (633nm)" package="5 mm [THT]"]
  LED6 = LED - 5mm [color="Red (633nm)" package="5 mm [THT]"]
  LED7 = LED - 5mm [color="Red (633nm)" package="5 mm [THT]"]
  LED8 = LED - 5mm [color="Red (633nm)" package="5 mm [THT]"]
  LED9 = LED - 5mm [color="Red (633nm)" package="5 mm [THT]"]
  LED10 = LED - 5mm [color="Red (633nm)" package="5 mm [THT]"]
  LED13 = LED - 5mm [color="Red (633nm)" package="5 mm [THT]"]
  LED14 = LED - 5mm [color="Red (633nm)" package="5 mm [THT]"]
  power = Battery
  push = Square Pushbutton
  toggle = Toggle Switch [package=THT]

nets:
  N1: LED1.cathode, LED1.anode, LED2.cathode, LED2.anode, LED3.cathode, LED3.anode, LED4.cathode, LED4.anode, LED5.cathode, LED5.anode, LED6.cathode, LED6.anode, LED7.anode, LED8.anode, LED9.anode, LED10.anode, LED13.anode, LED14.anode, power.+, toggle.COM
  N2: LED7.cathode, LED8.cathode, LED9.cathode, LED10.cathode, LED13.cathode, LED14.cathode, toggle.L2
  N3: power.-, push.leg0
  N4: push.leg1, toggle.L1
