# Fritzing sketch id1282___fritzing_semalari__daha_dun_annemizin_0 (saved by Fritzing 0.9.2b)
circuit board: 8.46667cm x 5.64444cm
breadboards: 1

parts:
  R1 = Resistor [tolerance=±5% resistance=220 package="1206 [SMD]"]
  J1 = Piezo Speaker
  Eleman1 = Arduino Uno (Rev3)

nets:
  N1: R1.Pin_0, Eleman1.GND
  N2: R1.Pin_1, J1.pin1
  N3: J1.pin2, Eleman1.D4
