# Fritzing sketch id1283_Daisy_Chain_Shift_Registers_RPi_0 (saved by Fritzing 0.9.1b)
breadboards: 1

parts:
  Raspberry_Pi1 = Raspberry Pi B rev2
  U1 = 74HC595 [package="DIP16 [THT]"]
  U2 = 74HC595 [package="DIP16 [THT]"]

nets:
  VCC: Raspberry_Pi1.3V3, U1.MR, U1.ST_CP, U1.VCC, U2.MR, U2.ST_CP, U2.VCC
  GND: Raspberry_Pi1.GND, U1.GND, U1.OE, U2.GND, U2.OE
  N1: Raspberry_Pi1.GPIO_22, U1.SH_CP, U2.SH_CP
  N2: Raspberry_Pi1.GPIO_25, U1.DS
  N3: U1.Q7', U2.DS
