# Fritzing sketch id1284_Dancing_Towards_Light_Dress_Fritzing_Diagram_0 (saved by Fritzing 0.9.0b)

parts:
  Part1 = LilyPad Arduino Simple Board
  Part2 = LilyPad LED
  Part3 = LilyPad LED
  Part4 = LilyPad LED
  Part5 = LilyPad LED
  Part6 = LilyPad LED
  Part7 = LilyPad LED
  Part8 = LilyPad Accelerometer ADXL335
  Part9 = LilyPad LED
  Part10 = LilyPad LED
  Part13 = LilyPad LED
  Part14 = LilyPad LED
  Part15 = LilyPad LED
  Part16 = LilyPad LED
  Part18 = LilyPad LED
  BAT1 = Battery Holders [package=lipo-1100mAh]  # not connected

nets:
  N1: Part1.A2, Part9.+
  N2: Part1.A3, Part8.XOUT
  N3: Part1.A4, Part8.YOUT
  N4: Part1.A5, Part8.ZOUT
  N5: Part1.D11, Part6.+, Part14.+, Part15.+, Part16.+, Part18.+
  N6: Part1.D6, Part7.+
  N7: Part1.D9, Part4.+
  N8: Part1.D10, Part3.+, Part10.+, Part13.+
  N9: Part1.D5, Part2.+, Part5.+
  N10: Part1.GND, Part2.-, Part8.COM, Part9.-, Part10.-, Part13.-
  VCC: Part1.VCC, Part8.5V
  N11: Part3.-, Part5.-, Part7.-
  N12: Part6.-, Part14.-, Part15.-, Part16.-, Part18.-

notes:
  Electrical wire used as insulator
