# Fritzing sketch id1286_Dark_Detector_1_0 (saved by Fritzing 0.9.2b)
breadboards: 1

parts:
  U1 = 555 Timer [package="DIP8 [THT]"]
  C1 = Electrolytic Capacitor [capacitance=100nF package="100 mil [THT, electrolytic]"]
  R1 = Resistor [tolerance=±5% resistance=100k package=THT]
  R2 = Resistor [tolerance=±5% resistance=10k package=THT]
  R3 = Resistor [tolerance=±5% resistance=22k package=THT]
  Q1 = PNP-Transistor [package="TO92 [THT]"]
  R4 = Photocell (LDR) [package=THT]
  SP1 = SPEAKER [package=pcb_mount_speaker]
  VCC1 = Battery block 9V

nets:
  N1: U1.Ground, C1.-, Q1.C, R4.pin_1, VCC1.-
  N2: U1.Trigger, U1.Threshold, C1.+, R2.Pin_1
  N3: U1.Output, Q1.B
  N4: U1.Reset, R1.Pin_0, R4.pin_0
  N5: U1.Discharge, R2.Pin_0, R3.Pin_0
  N6: U1.Vcc_Supply_Voltage, R1.Pin_1, R3.Pin_1, SP1.-
  N7: Q1.E, SP1.+
