# Fritzing sketch id1287_Untitled_Sketch_0 (saved by Fritzing 0.7.12b)
breadboards: 1

parts:
  Q1 = NPN-Transistor [package="TO92 [THT]"]
  R2 = Rotary Potentiometer (Small) [maximum_resistance=100kΩ]
  R3 = Photocell (LDR) [package=THT]
  LED1 = white smd LED [package="0603 [SMD]"]
  VCC1 = Battery block 9V
  R4 = 1k Ω Resistor [package=THT]

nets:
  N1: Q1.E, LED1.anode
  N2: Q1.B, R2.leg1, R3.pin_0
  N3: Q1.C, VCC1.+, R4.Pin_0
  N4: R3.pin_1, LED1.cathode, VCC1.-
