# Fritzing sketch id1288_Dark_sensor_using_555_timer_0 (saved by Fritzing 0.7.11b)
breadboards: 1

parts:
  U1 = 555 Timer [package="DIP8 [THT]"]
  R4_47k = Resistor [tolerance=±5% resistance=47k package=THT]
  R1 = Photocell (LDR) [package=THT]
  R2_47k = Resistor [tolerance=±5% resistance=47k package=THT]
  R3_470Ω = Resistor [tolerance=±5% resistance=470 package=THT]
  C1_100uF = Electrolytic Capacitor [capacitance=10µF voltage=20V package="100 mil [THT, electrolytic]"]
  LED1 = LED - 5mm [color="Red (633nm)" package="5 mm [THT]"]
  C2_100nF = Ceramic Capacitor [capacitance=100nF package="100 mil [THT, multilayer]"]
  VCC1_6v = Battery

nets:
  N1: U1.Ground, R4_47k.Pin_1, C1_100uF.+, LED1.cathode, C2_100nF.1, VCC1_6v.-
  N2: U1.Trigger, R4_47k.Pin_0, R1.pin_1
  N3: U1.Output, R3_470Ω.Pin_0
  N4: U1.Reset, U1.Vcc_Supply_Voltage, R1.pin_0, R2_47k.Pin_0, VCC1_6v.+
  N5: U1.Control_Voltage, C2_100nF.0
  N6: U1.Threshold, U1.Discharge, R2_47k.Pin_1, C1_100uF.-
  N7: R3_470Ω.Pin_1, LED1.anode
