# Fritzing sketch id1289_DARLINGTON_0 (saved by Fritzing 0.3.19b)
breadboards: 1

parts:
  VCC1 = obsolete Battery
  Q1 = NPN-Transistor [package="TO92 [THT]"]
  Q2 = NPN-Transistor [package="TO92 [THT]"]
  R1 = Resistor [resistance=220k package=THT]
  LED1 = Red LED - 5mm
  R2 = Resistor [resistance=1k package=THT]
  S1 = Toggle Switch [package=THT]
  J1 = female pin header, 1 pin [form="♂ (male)"]
  J3 = female pin header, 1 pin [form="♂ (male)"]

nets:
  N1: VCC1.-, Q2.E
  N2: VCC1.+, S1.L1, J3.pin1
  N3: Q1.E, Q2.B
  N4: Q1.B, R1.Pin_1
  N5: Q1.C, Q2.C, LED1.cathode
  N6: R1.Pin_0, J1.pin1
  N7: LED1.anode, R2.Pin_0
  N8: R2.Pin_1, S1.COM

notes:
  "Darlington pair" - while holding one finger to the male connector by the 220K resistor, touch the male connector by the positive terminal - the LED should light up.
  DARLINGTON
