# Fritzing sketch id128_Atomizer48VMosfetCircuit_0 (saved by Fritzing 0.9.1b)
breadboards: 1

parts:
  Part3 = Arduino Uno (Rev3)
  48V_Supply5 = mystery part, 3 pins [chip_label=?]
  R9 = Resistor [tolerance=±5% resistance=10k package=THT]  # not connected
  R10 = Resistor [tolerance=±5% resistance=10k package=THT]  # not connected
  Q10 = Basic FET P-Channel [package="TO220 [THT]"]  # not connected
  U4 = mystery part, 3 pins [chip_label=?]  # not connected
  Q11 = NPN-Transistor [package="TO92 [THT]"]  # not connected
  Power_plug1 = Power plug  # not connected

nets:
  N1: Part3.GND, 48V_Supply5.pin3

notes:
  48V Supply
  48V Atomizer
