# Fritzing sketch id1290_Untitled_Sketch_0 (saved by Fritzing 0.9.1b)
breadboards: 1

parts:
  Part1 = Arduino Ethernet Shield (Rev3)
  R1 = Resistor [tolerance=±5% resistance=220 package=THT]
  R2 = Resistor [tolerance=±5% resistance=220 package=THT]

nets:
  N1: Part1.A3, Part1.A4/SDA, Part1.5V, R1.Pin_1, R2.Pin_0
  N2: Part1.GND, R1.Pin_0, R2.Pin_1
