# Fritzing sketch id1292_Night_and_Day_Photo_Cell_1.1_0 (saved by Fritzing 0.9.2b)
circuit board: 8.46667cm x 5.64444cm
breadboards: 1

parts:
  R1 = Resistor [tolerance=±5% resistance=68k package=THT]
  R2 = PHOTOCELL [package=photocell]
  R3 = Resistor [tolerance=±5% resistance=100k package=THT]
  Q1 = NPN-Transistor [part_number="2N4401 NPN" package="TO92 [THT]"]
  R4 = Resistor [tolerance=±5% resistance=330 package=THT]
  Q2 = PNP-Transistor [part_number=2N3906 package="TO92 [THT]"]
  R5 = Resistor [tolerance=±5% resistance=330 package=THT]
  Q3 = NPN-Transistor [part_number=PN2222 package="TO92 [THT]"]
  R6 = Resistor [tolerance=±5% resistance=10k package=THT]

nets:
  N1: R1.Pin_0, R2.P$1, R3.Pin_1, Q1.B
  N2: R1.Pin_1, Q2.C
  N3: R2.P$2, Q1.E, Q3.E, Q3.C, R6.Pin_1
  N4: R3.Pin_0, Q2.E, R5.Pin_1
  N5: Q1.C, R4.Pin_1
  N6: R4.Pin_0, Q2.B
  N7: R5.Pin_0, Q3.B, R6.Pin_0
