# Fritzing sketch id1297_Sound_Detector_analog_(2)_0 (saved by Fritzing 0.8.7b)
breadboards: 1

parts:
  D1 = LED_BARGRAPH_10 [package=led_bargaph_10]
  IC2 = LM3914
  R6 = Resistor [tolerance=±5% resistance=220 package=THT]
  U1 = Voltage Regulator - Variable [package="TO220 [THT]"]
  C3 = Capacitor Polarized [package=panasonic_c]
  C4 = Capacitor Polarized [package=panasonic_c]
  R7 = Resistor [tolerance=±5% resistance=33k package=THT]
  R8 = Resistor [tolerance=±5% resistance=100k package=THT]
  R9 = Resistor [tolerance=±5% resistance=2.2k package=THT]
  PART1 = prefix0000_MIC-12642
  R10 = Resistor [tolerance=±5% resistance=680 package=THT]

nets:
  5V: D1.A_A, D1.B_A, D1.C_A, D1.D_A, D1.E_A, D1.F_A, D1.G_A, D1.H_A, D1.I_A, D1.J_A, R6.Pin_0, U1.OUT, C3.+, PART1.connector3
  N1: D1.J_C, IC2.connector0
  N2: D1.I_C, IC2.connector17
  N3: D1.H_C, IC2.connector16
  N4: D1.G_C, IC2.connector15
  N5: D1.F_C, IC2.connector14
  N6: D1.E_C, IC2.connector13
  N7: D1.D_C, IC2.connector12
  N8: D1.C_C, IC2.connector11
  N9: D1.B_C, IC2.connector10
  N10: D1.A_C, IC2.connector9
  GND: IC2.connector1, IC2.connector3, C3.-, C4.-, R7.Pin_0, PART1.connector4, R10.Pin_0
  13V: IC2.connector2, IC2.connector8, U1.IN, C4.+
  N11: IC2.connector4, PART1.connector1
  N12: IC2.connector5, R8.Pin_1
  N13: IC2.connector6, R8.Pin_0, R9.Pin_0
  N14: IC2.connector7, R7.Pin_1, R9.Pin_1
  N15: R6.Pin_1, U1.ADJ, R10.Pin_1
