# Fritzing sketch id1299_DC_IV_Input_02_Potentiometer_0 (saved by Fritzing 0.9.1b)
breadboards: 1

parts:
  R1 = Rotary Potentiometer (Small) [maximum_resistance=100kΩ package=THT]
  Part1 = Arduino Uno (Rev3)

nets:
  N1: R1.leg1, Part1.5V
  N2: R1.wiper, Part1.A0
  N3: R1.leg2, Part1.GND
