# Fritzing sketch id12_Reed_Switch_0 (saved by Fritzing 0.9.1b)
breadboards: 1

parts:
  S1 = Reed switch [package=THT]
  R1 = Resistor [tolerance=±5% resistance=220 package=THT]
  R2 = Resistor [tolerance=±5% resistance=10k package=THT]
  Componente1 = Arduino Uno (Rev3)
  LED1 = LED - 5mm [color="Red (633nm)" package="5 mm [THT]"]

nets:
  N1: S1.pin_1, R2.Pin_1, Componente1.D12/MISO
  N2: S1.pin_2, Componente1.5V
  N3: R1.Pin_0, R2.Pin_0, Componente1.GND
  N4: R1.Pin_1, LED1.cathode
  N5: Componente1.D9_PWM, LED1.anode
