# Fritzing sketch id1300_dc_motor_devre_0 (saved by Fritzing 0.9.3b)

parts:
  M1 = DC Motor
  M2 = DC Motor
  Parça4 = Arduino Uno (Rev3) - ICSP
  S1 = Ponte-H L298N
  BAT1 = BC9VPC [package=bc9vpc]

nets:
  N1: M1.pin_1, S1.connector14
  N2: M1.pin_2, S1.connector13
  N3: M2.pin_1, S1.connector11
  N4: M2.pin_2, S1.connector10
  N5: Parça4.D9_PWM, S1.connector8
  N6: Parça4.D10_PWM/SS, S1.connector7
  N7: Parça4.GND, S1.connector2, BAT1.V-
  N8: Parça4.D5_PWM, S1.connector5
  N9: Parça4.D6_PWM, S1.connector6
  N10: Parça4.5V, S1.connector3
  N11: S1.connector1, BAT1.V+
