# Fritzing sketch id1301_VibrationMotorController3_0 (saved by Fritzing 0.7.12b)
breadboards: 1

parts:
  C1 = Ceramic Capacitor [capacitance=100nF package="100 mil [THT, multilayer]"]
  D1 = Rectifier Diode [part_number=1N4001 package="300 mil [THT]"]
  M1 = DC Motor
  VCC1 = Battery block 9V
  Q1 = NPN-Transistor [package="TO92 [THT]"]
  R1 = 1k Ω Resistor [package=THT]
  Arduino1 = Arduino

nets:
  N1: C1.0, D1.cathode, M1.pin_1, VCC1.+
  N2: C1.1, D1.anode, M1.pin_2, Q1.E
  N3: VCC1.-, Q1.B, Arduino1.GND
  N4: Q1.C, R1.Pin_1
  N5: R1.Pin_0, Arduino1.A0
