# Fritzing sketch id1302_DC_Motor_Reversing_(EDIT)_0 (saved by Fritzing 0.9.0b)
breadboards: 1

parts:
  Arduino_UNO = Arduino Uno (Rev3)
  LCD_Module_(16x2) = LCD-16X2 [package=lcd-16x2_noholes]
  Pot_1 = Rotary Potentiometer (Small) [maximum_resistance=100kΩ package=THT]
  L293N = L293D [package=THT]
  Switch_1 = Pushbutton [package="[THT]"]
  Pot_2 = Rotary Potentiometer (Small) [maximum_resistance=100kΩ package=THT]
  DC_Motor = DC Motor

nets:
  N1: Arduino_UNO.A0, Pot_2.wiper
  N2: Arduino_UNO.D8, L293N.In_2
  N3: Arduino_UNO.D9_PWM, L293N.In_1
  N4: Arduino_UNO.D10_PWM/SS, L293N.Enable_1
  N5: Arduino_UNO.D11_PWM/MOSI, LCD_Module_(16x2).E
  N6: Arduino_UNO.D12/MISO, LCD_Module_(16x2).RS
  GND: Arduino_UNO.GND, LCD_Module_(16x2).VSS, LCD_Module_(16x2).R_W, LCD_Module_(16x2).K, Pot_1.leg2, L293N.0V, Switch_1.Pin_1, Switch_1.Pin_2, Pot_2.leg2
  N7: Arduino_UNO.D2, LCD_Module_(16x2).DB7
  N8: Arduino_UNO.D3_PWM, LCD_Module_(16x2).DB6
  N9: Arduino_UNO.D4, LCD_Module_(16x2).DB5
  N10: Arduino_UNO.D5_PWM, LCD_Module_(16x2).DB4
  N11: Arduino_UNO.D7, Switch_1.Pin_3, Switch_1.Pin_4
  5V: Arduino_UNO.5V, LCD_Module_(16x2).VDD, LCD_Module_(16x2).A, Pot_1.leg1, L293N.+Vmotor, L293N.+V, Pot_2.leg1
  N12: LCD_Module_(16x2).VO, Pot_1.wiper
  N13: L293N.Out_1_(_Controlled_by_Enable_1_), DC_Motor.pin_2
  N14: L293N.Out_2_(_Controlled_by_Enable_1_), DC_Motor.pin_1
