# Fritzing sketch id1303_Untitled_Sketch_2_0 (saved by Fritzing 0.9.2b)
breadboards: 1

parts:
  Part1 = Arduino Uno (Rev3)
  M1 = DC Motor
  IC1 = H-Bridge [package=THT]
  R1 = Rotary Potentiometer (Small) [maximum_resistance=100kΩ package=THT]
  S1 = Pushbutton [package="[THT]"]
  R2 = Resistor [tolerance=±5% resistance=220 package=THT]

nets:
  N1: Part1.A0, R1.wiper
  N2: Part1.D8, S1.Pin_1, S1.Pin_2, R2.Pin_1
  N3: Part1.D9_PWM, IC1.2A
  N4: Part1.D10_PWM/SS, IC1.1A
  N5: Part1.D11_PWM/MOSI, IC1.1_2EN
  N6: Part1.5V, IC1.VCC1, R1.leg1, S1.Pin_3, S1.Pin_4
  GND: Part1.GND, IC1.GND1, IC1.GND2, IC1.VCC2, R1.leg2, R2.Pin_0
  N7: M1.pin_1, IC1.2Y
  N8: M1.pin_2, IC1.1Y
