# Fritzing sketch id1304_Act_4_0 (saved by Fritzing 0.9.3b)
breadboards: 1

parts:
  M1 = DC Motor
  Part1 = Arduino Uno (Rev3)
  LED1 = RGB LED (com. cathode, rgb) [package="5 mm [THT]"]
  S1 = Momentary Switch [package=tactile-pth]
  R1 = Resistor [tolerance=±5% resistance=10k package=THT]

nets:
  N1: M1.pin_1, Part1.D6_PWM
  N2: M1.pin_2, Part1.D5_PWM
  N3: Part1.GND, LED1.common_cathode, R1.Pin_0
  N4: Part1.D1/TX, S1.1, R1.Pin_1
  N5: Part1.D3_PWM, LED1.blue_anode
  N6: Part1.D4, LED1.red_anode
  N7: Part1.5V, S1.3
