# Fritzing sketch id1305_dc_moter_1_0 (saved by Fritzing 0.9.2b)

parts:
  M1 = DC Motor
  BAT1 = Battery Holders [package=battery-aa-kit]
  BAT2 = Battery Holders [package=battery-aa-kit]  # not connected
  BAT3 = Battery Holders [package=battery-aa-kit]
  M3 = DC Motor
  BAT4 = Battery Holders [package=battery-aa-kit]
  M4 = DC Motor
  M2 = DC Motor  # not connected

nets:
  N1: M1.pin_2, BAT1.-
  N2: BAT3.+, M3.pin_1
  N3: BAT3.-, M3.pin_2
  N4: BAT4.-, M4.pin_1

notes:
  停止その１
  停止その２
  正転
  逆転
