# Fritzing sketch id1306_dc_motor+ir_0 (saved by Fritzing 0.8.5b)
circuit board: 8.46667cm x 5.64444cm
breadboards: 1

parts:
  Parte1 = Arduino Uno (Rev3)
  R1 = Rotary Potentiometer (Small) [maximum_resistance=100kΩ package=THT]
  S1 = Pushbutton [package="[THT]"]
  S2 = Pushbutton [package="[THT]"]
  IC1 = L293D [package=THT]
  C1 = Electrolytic Capacitor [capacitance=100µF voltage=20V package="200 mil [THT, electrolytic]"]
  Parte2 = Max Power IR LED Kit
  BAT1 = BC9VPC [package=bc9vpc]
  M1 = DC Motor
  R2 = Resistor [tolerance=±5% resistance=10k package=THT]
  R3 = Resistor [tolerance=±5% resistance=10k package=THT]

nets:
  N1: Parte1.A0, R1.wiper
  N2: Parte1.D9_PWM, IC1.Enable_1
  N3: Parte1.D11_PWM/MOSI, Parte2.CONTROL
  N4: Parte1.D2, IC1.In_2
  N5: Parte1.D3_PWM, IC1.In_1
  N6: Parte1.D4, S1.Pin_1, S1.Pin_2, R2.Pin_0
  N7: Parte1.D5_PWM, S2.Pin_1, S2.Pin_2
  5V: Parte1.5V, S1.Pin_3, S1.Pin_4, S2.Pin_3, S2.Pin_4, IC1.+V, Parte2.VCC
  GND: Parte1.GND, R1.leg2, IC1.0V, Parte2.GND, BAT1.V+, R2.Pin_1, R3.Pin_1
  N8: R1.leg1, IC1.+Vmotor, BAT1.V-
  N9: IC1.Out_1_(_Controlled_by_Enable_1_), C1.-, M1.pin_1
  N10: IC1.Out_2_(_Controlled_by_Enable_1_), C1.+, M1.pin_2
