# Fritzing sketch id1307_DC_MOTOR_01_0 (saved by Fritzing 0.9.3b)
breadboards: 1

parts:
  부품1 = Arduino Uno (Rev3) - ICSP
  IC1 = L293D [package=THT]
  M1 = DC Motor

nets:
  N1: 부품1.5V, IC1.Enable_1, IC1.In_1, IC1.+Vmotor, IC1.+V
  N2: 부품1.GND, IC1.0V, IC1.In_2
  N3: IC1.Out_1_(_Controlled_by_Enable_1_), M1.pin_2
  N4: IC1.Out_2_(_Controlled_by_Enable_1_), M1.pin_1
