# Fritzing sketch id1307_motor_change_speed (saved by Fritzing 0.4.3b)
breadboards: 1

parts:
  M1 = DC Motor
  R1 = Rotary Potentiometer (Large) [package=THT]
  Power_plug1 = Power plug

nets:
  N1: M1.pin_1, R1.wiper
  N2: M1.pin_2, R1.leg2, Power_plug1.VCC
  N3: R1.leg1, Power_plug1.GND
