# Fritzing sketch id1308_DC_MOTOR_03_0 (saved by Fritzing 0.9.3b)
breadboards: 1

parts:
  부품1 = Arduino Uno (Rev3) - ICSP
  IC1 = L293D [package=THT]
  M1 = DC Motor
  U1 = POT [package=pot_mammoth]
  VCC1 = Battery
  R1 = Resistor [tolerance=±5% resistance=330 package="2010 [SMD]"]
  LED1 = LEDs [package=led10mm]
  LED2 = LEDs [package=led10mm]

nets:
  N1: 부품1.A0, U1.A
  N2: 부품1.GND, IC1.0V, U1.E, VCC1.-, R1.Pin_0, LED1.A, LED2.A
  N3: 부품1.D9_PWM, IC1.In_2
  N4: 부품1.D10_PWM/SS, IC1.In_1
  N5: 부품1.D11_PWM/MOSI, IC1.Enable_1
  N6: 부품1.5V, IC1.+V, U1.S
  N7: IC1.Out_1_(_Controlled_by_Enable_1_), M1.pin_2
  N8: IC1.Out_2_(_Controlled_by_Enable_1_), M1.pin_1
  N9: IC1.+Vmotor, VCC1.+
  N10: R1.Pin_1, LED1.C, LED2.C
