# Fritzing sketch id1309_DC_motor_0 (saved by Fritzing 0.7.1b)
breadboards: 1

parts:
  Arduino1 = Arduino
  R1 = Resistor [tolerance=±5% resistance=220 package=THT]
  Q1 = Basic FET N-Channel [package="TO220 [THT]"]
  M1 = DC Motor

nets:
  N1: Arduino1.GND, Q1.source
  N2: Arduino1.D9, Q1.gate
  N3: R1.Pin_0, Q1.drain, M1.pin_1
  N4: R1.Pin_1, M1.pin_2

notes:
  /*
  Speed up the motor
  This example shows how to control the speed of a DC motor an LED on pin 9
  using the analogWrite() function.
  This example based on the Arduino Example Fade sketch
  but modified to use timing instead of the delay() function
  */
  int turns = 0; // how fast the motor runs
  int turnAmount = 1; // how many turns the motor makes
  unsigned long currentTime;
  unsigned long loopTime;
  void setup() {
  // declare pin 9 to be an output:
  pinMode(9, OUTPUT);
  currentTime = millis();
  loopTime = currentTime;
  }
  void loop() {
  currentTime = millis();
  if(currentTime >= (loopTime + 20)){
  // set the speed of pin 9:
  analogWrite(9, turns);
  // change the turnings for next time through the loop:
  turns = turns + turnAmount;
  // speed up or slow down the motor
  if (turns == 0 || turns == 255) {
  turnAmount = -turnAmount ;
  }
  if (turns == 0) {
  delay(5000);
  }
  loopTime = currentTime; // Updates loopTime
  }
  // Other processing can be done here
  }
  Run a DC motor with your Arduino.
  - MOSFET
  - Resistor > 100ohm
  - Low V DC motor
