# Fritzing sketch id130_4Botones4leds2Motores_SamyHuerta_5xBuOgn_0 (saved by Fritzing 0.9.3b)
breadboards: 1

parts:
  Componente1 = Arduino Uno (Rev3)
  LED1 = LED - 5mm [color="Red (633nm)" package="5 mm [THT]"]  # not connected
  R1 = Resistor [tolerance=±5% resistance=220 package=THT]
  R2 = Resistor [tolerance=±5% resistance=10k package=THT]
  R3 = Resistor [tolerance=±5% resistance=10k package=THT]
  R4 = Resistor [tolerance=±5% resistance=10k package=THT]
  R5 = Resistor [tolerance=±5% resistance=10k package=THT]
  R6 = Resistor [tolerance=±5% resistance=220 package=THT]
  R7 = Resistor [tolerance=±5% resistance=220 package=THT]
  R8 = Resistor [tolerance=±5% resistance=220 package=THT]
  LED2 = LED - 5mm [color="Red (633nm)" package="5 mm [THT]"]
  LED3 = LED - 5mm [color="Red (633nm)" package="5 mm [THT]"]
  LED4 = LED - 5mm [color="Red (633nm)" package="5 mm [THT]"]
  S1 = Momentary Switch [package=ksa_sealed_tac_switch]
  S2 = Momentary Switch [package=ksa_sealed_tac_switch]
  S3 = Momentary Switch [package=ksa_sealed_tac_switch]
  S4 = Momentary Switch [package=ksa_sealed_tac_switch]
  S5 = Ponte-H L298N
  M1 = DC Motor
  M2 = DC Motor

nets:
  N1: Componente1.A1, R4.Pin_0, S4.4
  N2: Componente1.A2, R5.Pin_1, S1.3, S1.4
  N3: Componente1.A3, R3.Pin_1, S3.3
  N4: Componente1.A4/SDA, R2.Pin_0, S2.3, S2.4
  N5: Componente1.D8, S5.connector8
  N6: Componente1.D9_PWM, S5.connector7
  N7: Componente1.D10_PWM/SS, S5.connector6
  N8: Componente1.D11_PWM/MOSI, S5.connector5
  N9: Componente1.D3_PWM, LED4.anode
  N10: Componente1.D4, LED2.anode
  N11: Componente1.D5_PWM, LED3.anode
  N12: Componente1.5V, S3.4
  N13: Componente1.GND, R2.Pin_1, R4.Pin_1, R6.Pin_1, R7.Pin_1, R8.Pin_1, S1.1, S1.2
  N14: R1.Pin_0, R3.Pin_0, R5.Pin_0, S5.connector2
  N15: R6.Pin_0, LED3.cathode
  N16: R7.Pin_0, LED2.cathode
  N17: R8.Pin_0, LED4.cathode
  N18: S2.1, S2.2
  N19: S4.1, S5.connector1
  N20: S5.connector10, M2.pin_2
  N21: S5.connector11, M2.pin_1
  N22: S5.connector13, M1.pin_2
  N23: S5.connector14, M1.pin_1
