# Fritzing sketch id1310_DC_motor_control_with_Raspberry_Pi_0 (saved by Fritzing 0.9.2b)
breadboards: 1

parts:
  R1 = Resistor [tolerance=±5% resistance=220 package=THT]
  Raspberry_Pi2 = Raspberry Pi B+
  S1 = Pushbutton [package="[THT]"]
  R2 = 1K
  S2 = Momentary Switch [package=ksa_sealed_tac_switch]
  R3 = 1K
  Q1 = TRANSISTOR_NPN [package=to-92]
  M1 = DC Motor
  U1 = DIODE-ZENER [package=diode-zener]
  C1 = Electrolytic Capacitor [capacitance=1000μF package="1010 [SMD, electrolytic]"]

nets:
  N1: R1.Pin_0, Raspberry_Pi2.GPIO13
  N2: R1.Pin_1, Q1.B
  N3: Raspberry_Pi2.3v3, R2.connector0, R3.connector0, M1.pin_1, U1.C, C1.+
  N4: Raspberry_Pi2.GPIO19, S1.Pin_1, S1.Pin_2, R2.connector1
  N5: Raspberry_Pi2.GPIO26, S2.1, R3.connector1
  N6: Raspberry_Pi2.GND, S1.Pin_3, S1.Pin_4, S2.3, Q1.E, C1.-
  N7: Q1.C, M1.pin_2
