# Fritzing sketch id1311_Untitled_Sketch_0 (saved by Fritzing 0.9.3b)
breadboards: 1

parts:
  Part1 = Arduino Uno (Rev3)
  M1 = DC Motor
  IC1 = L293D [package=THT]
  Grove1 = Grove OLED 128x96
  R4 = Rotary Potentiometer (Small) [maximum_resistance=100kΩ package=THT]
  S1 = Pushbutton [package="[SMD]"]
  R6 = Resistor [tolerance=±5% resistance=10 package=THT]
  R7 = Resistor [tolerance=±5% resistance=10 package=THT]
  R8 = Resistor [tolerance=±5% resistance=10 package=THT]
  LED1 = smd LED [color="Red (633nm)" package="0603 [SMD]"]
  LED2 = smd LED [color="Yellow (585nm)" package="0603 [SMD]"]

nets:
  N1: Part1.A0, R4.wiper
  N2: Part1.A4/SDA, Grove1.SDA
  N3: Part1.A5/SCL, Grove1.SCL
  N4: Part1.D9_PWM, IC1.In_3
  N5: Part1.D10_PWM/SS, IC1.In_4
  N6: Part1.D11_PWM/MOSI, IC1.+V
  N7: Part1.D2, R8.Pin_1
  N8: Part1.D3_PWM, R7.Pin_1
  N9: Part1.D7, IC1.+Vmotor, Grove1.VCC, R4.leg2, S1.Pin_3, S1.Pin_4
  N10: M1.pin_1, IC1.Out_3_(_Controlled_by_Enable_2_)
  N11: M1.pin_2, IC1.Out_4_(_Controlled_by_Enable_2_)
  N12: IC1.Enable_2, Grove1.GND, R4.leg1, R6.Pin_1, LED1.cathode, LED2.cathode
  N13: S1.Pin_1, S1.Pin_2, R6.Pin_0
  N14: R7.Pin_0, LED1.anode
  N15: R8.Pin_0, LED2.anode
