# Fritzing sketch id1312_Projekt_Auto_0 (saved by Fritzing 0.9.3b)
breadboards: 1

parts:
  Part1 = Arduino Uno (Rev3)
  IC1 = L293D [package=THT]
  M2 = DC Motor
  Part2 = Bluetooth HC-05 Macho
  M3 = DC Motor
  VCC1 = Battery block 9V
  VCC2 = Battery
  VCC3 = Battery

nets:
  N1: Part1.D0/RX, Part2.TXD
  N2: Part1.D1/TX, Part2.RXD
  N3: Part1.D2, IC1.In_1
  N4: Part1.D3_PWM, IC1.In_2
  N5: Part1.D4, IC1.In_3
  N6: Part1.D5_PWM, IC1.In_4
  N7: Part1.VIN, IC1.+Vmotor, VCC1.+, VCC2.+, VCC3.+
  N8: IC1.Enable_1, IC1.Enable_2, IC1.+V, Part2.VCC
  N9: IC1.Out_1_(_Controlled_by_Enable_1_), M3.pin_1
  N10: IC1.0V, Part2.GND, VCC1.-, VCC2.-, VCC3.-
  N11: IC1.Out_2_(_Controlled_by_Enable_1_), M3.pin_2
  N12: IC1.Out_3_(_Controlled_by_Enable_2_), M2.pin_1
  N13: IC1.Out_4_(_Controlled_by_Enable_2_), M2.pin_2
