# Fritzing sketch id1313_dc_meter_0 (saved by Fritzing 0.9.3b)
breadboards: 1

parts:
  ACS709_Stromsensor_Breakout_Board_-75_to_+75A1 = ACS709_Stromsensor_Breakout_Board__75_to__75A
  Componente1 = Arduino Yun
  R1 = Resistor [tolerance=±5% resistance=10k package="1206 [SMD]"]
  R2 = Resistor [tolerance=±5% resistance=100k package="0805 [SMD]"]
  J1 = Screw terminal - 2 pins [package=THT]
  J2 = Screw terminal - 2 pins [package=THT]
  J3 = Screw terminal - 2 pins [package=THT]
  ASA01A18-LS1 = prefix0000

nets:
  N1: ACS709_Stromsensor_Breakout_Board_-75_to_+75A1.connector0, R2.Pin_1, J2.pin1, J2.pin2, ASA01A18-LS1.connector2, ASA01A18-LS1.connector3
  N2: ACS709_Stromsensor_Breakout_Board_-75_to_+75A1.connector1, J1.pin1, J1.pin2
  N3: ACS709_Stromsensor_Breakout_Board_-75_to_+75A1.connector7, Componente1.A0
  N4: ACS709_Stromsensor_Breakout_Board_-75_to_+75A1.connector8, Componente1.VIN, ASA01A18-LS1.connector6
  N5: ACS709_Stromsensor_Breakout_Board_-75_to_+75A1.connector9, Componente1.GND, R1.Pin_0, J3.pin1, J3.pin2, ASA01A18-LS1.connector0, ASA01A18-LS1.connector1, ASA01A18-LS1.connector7
  N6: Componente1.A1, R1.Pin_1, R2.Pin_0

notes:
  orange= BATT in
  purple = BATT out
  black = GND
  DC power smart meter
  with voltage and current sensors
