# Fritzing sketch id1314_PowerSupply_0 (saved by Fritzing 0.9.2b)
circuit board: 10.856cm x 6.12143cm
breadboards: 1

parts:
  J1 = ATX24 Pin Power Supply Connector [package=atx24_right_angle]
  J2 = COMPUTER-PERIPHERAL-POWER [package=computer-peripheral-power]
  J3 = COMPUTER-PERIPHERAL-POWER [package=computer-peripheral-power]
  J4 = COMPUTER-PERIPHERAL-POWER [package=computer-peripheral-power]
  J5 = COMPUTER-PERIPHERAL-POWER [package=computer-peripheral-power]
  J6 = BANANA_CONN [package=banana_conn]
  J7 = BANANA_CONN [package=banana_conn]
  J8 = BANANA_CONN [package=banana_conn]
  J9 = BANANA_CONN [package=banana_conn]
  J10 = BANANA_CONN [package=banana_conn]
  J11 = BANANA_CONN [package=banana_conn]
  U1 = Voltage Regulator [package=to220-adj]
  R1 = Rotary Potentiometer (Large) [maximum_resistance=10kΩ package=THT]
  R2 = Resistor [tolerance=±5% resistance=330 package=THT]
  R3 = Resistor [tolerance=±5% resistance=150 package=THT]
  S1 = Toggle Switch [package=THT]
  LED3 = LED - 5mm [color="Red (633nm)" package="5 mm [THT]"]
  LED4 = LED - 5mm [color="Red (633nm)" package="5 mm [THT]"]
  R4 = Resistor [tolerance=±5% resistance=150 package=THT]
  C3 = Electrolytic Capacitor [capacitance=1µF voltage=50V package="100 mil [THT, electrolytic]"]
  C4 = Tantalum Capacitor [capacitance=0.1µF voltage=35V package="100 mil [THT, tantalum]"]

nets:
  N1: J1.3.3V, J8.1
  GND: J1.GND, J1.NC, J2.GND, J2.NC, J3.GND, J3.NC, J4.GND, J4.NC, J5.GND, J5.NC, J6.1, R1.wiper, S1.COM, LED3.cathode, LED4.cathode, C3.-, C4.-
  5V: J1.5V, J2.5V, J3.5V, J4.5V, J5.5V, J7.1
  N2: J1.PWR_OK, R3.Pin_0
  N3: J1.5V_STDBY, R4.Pin_0
  12V: J1.12V, J2.12V, J3.12V, J4.12V, J5.12V, J10.1, U1.IN, C4.+
  N4: J1.-12V, J9.1
  N5: J1.PS_ON, S1.L2
  N6: J11.1, U1.OUT, R2.Pin_0, C3.+
  N7: U1.ADJ, R1.leg2, R2.Pin_1
  N8: R3.Pin_1, LED3.anode
  N9: LED4.anode, R4.Pin_1

notes:
  GND
  3.3 V
  5.0 V
  -12.0V
  12.0V
  0 - 12 V
  PRW_ON
  STDB
  PWD_SW
