# Fritzing sketch id1315_Motor_Speed_Controller_0 (saved by Fritzing 0.8.5b)
circuit board: 10cm x 5.99996cm
breadboards: 1

parts:
  U1 = 74HC595 [package="DIP16 [THT]"]
  Q1 = NPN-Transistor [package="TO92 [THT]"]
  M1 = DC Motor
  S1 = Pushbutton [package="[THT]"]
  S2 = Pushbutton [package="[THT]"]
  D1 = Rectifier Diode [part_number=1N4001 package="300 mil [THT]"]
  R1 = Resistor [tolerance=±5% resistance=220 package=THT]
  R2 = Resistor [tolerance=±5% resistance=10k package=THT]
  7_Segment1 = 7 Segment Display
  R3 = Resistor [tolerance=±5% resistance=220 package=THT]
  R4 = Resistor [tolerance=±5% resistance=10k package=THT]
  R5 = Resistor [tolerance=±5% resistance=10k package=THT]
  Part1 = Arduino Leonardo (Rev3b)
  Power_plug1 = Power plug

nets:
  N1: U1.Q1, 7_Segment1.Segment_DP
  N2: U1.Q2, 7_Segment1.Segment_G
  N3: U1.Q3, 7_Segment1.Segment_F
  N4: U1.Q4, 7_Segment1.Segment_E
  N5: U1.Q5, 7_Segment1.Segment_D
  N6: U1.Q6, 7_Segment1.Segment_C
  N7: U1.Q7, 7_Segment1.Segment_B
  GND: U1.GND, U1.OE, Q1.E, S1.Pin_1, S1.Pin_2, S2.Pin_1, S2.Pin_2, R2.Pin_1, R3.Pin_0, Part1.GND, Power_plug1.GND
  VCC: U1.MR, U1.VCC, R4.Pin_1, R5.Pin_1, Part1.5V
  N8: U1.SH_CP, Part1.D5_PWM
  N9: U1.ST_CP, Part1.D4/A6
  N10: U1.DS, Part1.D6_PWM/A7
  N11: U1.Q0, 7_Segment1.Segment_A
  N12: Q1.B, R1.Pin_1, R2.Pin_0
  N13: Q1.C, M1.pin_1, D1.anode
  N14: M1.pin_2, D1.cathode, Power_plug1.VCC
  N15: S1.Pin_3, S1.Pin_4, R4.Pin_0, Part1.D3_PWM/SCL
  N16: S2.Pin_3, S2.Pin_4, R5.Pin_0, Part1.D2/SDA
  N17: R1.Pin_0, Part1.D9_PWM/A9
  N18: 7_Segment1.common_cathode, R3.Pin_1
