# Fritzing sketch id1316_DCF77_Uhr2_0 (saved by Fritzing 0.7.10b)
perfboards: 1

parts:
  7_Segment5 = 7 Segment Display
  7_Segment6 = 7 Segment Display
  7_Segment7 = 7 Segment Display
  7_Segment8 = 7 Segment Display
  HEF1 = HEF4094 [package="DIP16 [THT]"]
  R1 = Resistor [tolerance=±5% resistance=220 package=THT]
  R2 = Resistor [tolerance=±5% resistance=220 package=THT]
  R3 = Resistor [tolerance=±5% resistance=220 package=THT]
  R5 = Resistor [tolerance=±5% resistance=220 package=THT]
  R6 = Resistor [tolerance=±5% resistance=220 package=THT]
  R7 = Resistor [tolerance=±5% resistance=220 package=THT]
  R8 = Resistor [tolerance=±5% resistance=220 package=THT]
  R9 = Resistor [tolerance=±5% resistance=220 package=THT]
  IC1 = IC, DIP package, 14 pins [chip_label=ATTiny44]
  DCF1 = mystery_part_sip_4_100mil.fzp
  VCC1 = 4 x AAA Battery Mount
  R10 = Resistor [tolerance=±5% resistance=10k package=THT]

nets:
  N1: 7_Segment5.Segment_G, 7_Segment6.Segment_G, 7_Segment7.Segment_G, 7_Segment8.Segment_G, R2.Pin_0
  N2: 7_Segment5.Segment_F, 7_Segment6.Segment_F, 7_Segment7.Segment_F, 7_Segment8.Segment_F, R1.Pin_0
  N3: 7_Segment5.common_anode, IC1.pin6
  N4: 7_Segment5.Segment_E, 7_Segment6.Segment_E, 7_Segment7.Segment_E, 7_Segment8.Segment_E, R7.Pin_0
  N5: 7_Segment5.Segment_D, 7_Segment6.Segment_D, 7_Segment7.Segment_D, 7_Segment8.Segment_D, R5.Pin_0
  N6: 7_Segment5.Segment_DP, 7_Segment6.Segment_DP, 7_Segment7.Segment_DP, 7_Segment8.Segment_DP, R6.Pin_0
  N7: 7_Segment5.Segment_C, 7_Segment6.Segment_C, 7_Segment7.Segment_C, 7_Segment8.Segment_C, R8.Pin_0
  N8: 7_Segment5.Segment_B, 7_Segment7.Segment_B, 7_Segment8.Segment_B, R9.Pin_0
  N9: 7_Segment5.Segment_A, 7_Segment6.Segment_A, 7_Segment7.Segment_A, 7_Segment8.Segment_A, R3.Pin_0
  N10: 7_Segment6.common_anode, IC1.pin5
  N11: 7_Segment7.common_anode, IC1.pin3
  N12: 7_Segment8.common_anode, IC1.pin2
  N13: HEF1.STROBE, HEF1.Vdd, IC1.pin1, DCF1.connector0, VCC1.+
  N14: HEF1.DATA, IC1.pin12
  N15: HEF1.CLOCK, IC1.pin11
  N16: HEF1.Q1, R3.Pin_1
  N17: HEF1.Q2, R9.Pin_1
  N18: HEF1.Q3, R8.Pin_1
  N19: HEF1.Q4, R5.Pin_1
  N20: HEF1.Vss, IC1.pin14, DCF1.connector1, DCF1.connector3, VCC1.-, R10.Pin_1
  N21: HEF1.Q8, R6.Pin_1
  N22: HEF1.Q7, R2.Pin_1
  N23: HEF1.Q6, R1.Pin_1
  N24: HEF1.Q5, R7.Pin_1
  N25: HEF1.OE, IC1.pin10
  N26: IC1.pin7, DCF1.connector2, R10.Pin_0
