# Fritzing sketch id1317_TOT_0 (saved by Fritzing 0.9.3b)
breadboards: 1

parts:
  Part1 = Soil Moisture Sensor
  Part2 = Soil Moisture Sensor
  Part3 = Soil Moisture Sensor
  M1 = DC Motor
  LED1 = LED - 3mm [color="Red (633nm)" package="3 mm [THT]"]
  LED2 = LED - 3mm [color="Red (633nm)" package="3 mm [THT]"]
  LED3 = LED - 3mm [color="Red (633nm)" package="3 mm [THT]"]
  R1 = Resistor [tolerance=±5% resistance=220 package="2010 [SMD]"]
  Part4 = Arduino Uno (Rev3)
  R2 = Resistor [tolerance=±5% resistance=220 package="2512 [SMD]"]
  R3 = Resistor [tolerance=±5% resistance=220 package="2512 [SMD]"]
  J1 = Piezo Speaker
  D1 = Zener Diode [part_number=1N4732A breakdown_voltage=3.6V package="300 mil [THT]"]
  Q1 = NPN-Transistor [package="SOT-23 [SMD]"]  # not connected
  R4 = Resistor [tolerance=±5% resistance=220 package="0805 [SMD]"]

nets:
  GND: Part1.GND, Part3.GND, Part4.GND, R2.Pin_1, R3.Pin_1, J1.pin1
  N1: Part1.SIG, Part4.A0
  VCC: Part1.VCC, Part2.VCC, Part3.VCC, M1.pin_1, Part4.5V, D1.cathode
  N2: Part2.SIG, Part4.A1
  N3: Part3.SIG, Part4.A2
  N4: M1.pin_2, D1.anode
  N5: LED1.cathode, Part4.D11_PWM/MOSI
  N6: LED1.anode, R3.Pin_0
  N7: LED2.cathode, Part4.D13/SCK
  N8: LED2.anode, R1.Pin_0
  N9: LED3.cathode, Part4.D12/MISO
  N10: LED3.anode, R2.Pin_0
  N11: Part4.D8, R4.Pin_1
  N12: Part4.D9_PWM, J1.pin2
