# Fritzing sketch id1319_AD9851_ARDUINO_0 (saved by Fritzing 0.9.2b)

parts:
  Часть1 = Arduino Uno (Rev3)
  Matrix_keypad2 = CMG
  LCD1 = LCD screen
  R1 = Resistor [tolerance=±5% resistance=20 package=THT]
  R2 = Rotary Potentiometer (Small) [maximum_resistance=10kΩ package=THT]
  AD1 = DDS AD9850

nets:
  N1: Часть1.A0, LCD1.DB1
  N2: Часть1.A1, LCD1.DB6
  N3: Часть1.A2, LCD1.DB7
  N4: Часть1.A3, LCD1.LED+
  N5: Часть1.A4/SDA, LCD1.LED-
  N6: Часть1.D8, Matrix_keypad2.connector26
  N7: Часть1.D9_PWM, Matrix_keypad2.connector25
  N8: Часть1.D10_PWM/SS, AD1.connector28
  N9: Часть1.D11_PWM/MOSI, AD1.connector29
  N10: Часть1.D12/MISO, AD1.connector30
  N11: Часть1.D13/SCK, LCD1.DB0
  N12: Часть1.D2, Matrix_keypad2.connector32
  N13: Часть1.D3_PWM, Matrix_keypad2.connector31
  N14: Часть1.D4, Matrix_keypad2.connector30
  N15: Часть1.D5_PWM, Matrix_keypad2.connector29
  N16: Часть1.D6_PWM, Matrix_keypad2.connector28
  N17: Часть1.D7, Matrix_keypad2.connector27
  N18: Часть1.5V, R1.Pin_1
  N19: LCD1.VSS, R1.Pin_0
  N20: LCD1.VDD, LCD1.V0, LCD1.E
  N21: LCD1.R/W, R2.wiper

notes:
  D7 D6 D5 D4 ......E R/W RS V0 K A
  Мой LCD WINSTAR WH1602A
  контрастность R10K
  Плату купил на EBAY M/C AD9851
  Генератор на плате 30.000 MHZ
  Программа для ARDUINO
  После загрузки на LCD строка "Hello,DDS!"
  Нажмите '*' появится строка "MHZ..."
  Введите нужное число мегагерц
  нажмите '#'
  появится строка "KHZ..."
  Введите нужное число килогерц
  нажмите '#'
  появится строка "HZ..."
  Введите нужное число герц
  нажмите '#'
  появится строка "F = XXXXXXX " c выбранной вами частотой
  Для изменения частоты нажмите '*' и повторите ввод нужного
  значения частоты
