# Fritzing sketch id1320_Debounced_button_on_internal_pullup_0 (saved by Fritzing 0.9.3b)
circuit board: 14.4683cm x 7.68033cm
breadboards: 1

parts:
  Arduino_Mega_2560_Rev3 = Arduino Mega 2560 (Rev3)
  S1 = Pushbutton [package="[THT]"]
  R1 = Resistor [tolerance=±5% resistance=220 package=THT]
  LED1 = LED - 5mm [color="Red (633nm)" package="5 mm [THT]"]

nets:
  N1: Arduino_Mega_2560_Rev3.D12_PWM, R1.Pin_0
  N2: Arduino_Mega_2560_Rev3.GND, S1.Pin_3, S1.Pin_4, LED1.cathode
  N3: Arduino_Mega_2560_Rev3.D2_PWM, S1.Pin_1, S1.Pin_2
  N4: R1.Pin_1, LED1.anode
