# Fritzing sketch id1321_ferramenta_de_giorgio_0 (saved by Fritzing 0.8.7b)
circuit board: 8.46667cm x 5.64444cm
breadboards: 1

parts:
  S1 = Pushbutton [package="[THT]"]
  S2 = Pushbutton [package="[THT]"]
  S3 = Pushbutton [package="[THT]"]
  S4 = Pushbutton [package="[THT]"]
  S5 = Pushbutton [package="[THT]"]
  arduino_1 = Arduino Uno (Rev3)
  R1 = Resistor [tolerance=±5% resistance=10k package=THT]
  R2 = Resistor [tolerance=±5% resistance=10k package=THT]
  R3 = Resistor [tolerance=±5% resistance=10k package=THT]
  R4 = Resistor [tolerance=±5% resistance=10k package=THT]
  R5 = Resistor [tolerance=±5% resistance=10k package=THT]
  LED1 = LED - 5mm [color="Red (633nm)" package="5 mm [THT]"]
  R6 = Resistor [tolerance=±5% resistance=220 package=THT]
  R7 = Resistor [tolerance=±5% resistance=220 package=THT]
  LED2 = LED - 5mm [color="Blue (525nm)" package="5 mm [THT]"]
  R8 = Resistor [tolerance=±5% resistance=220 package=THT]
  LED3 = LED - 5mm [color="Green (570nm)" package="5 mm [THT]"]
  R9 = Resistor [tolerance=±5% resistance=220 package=THT]
  LED4 = LED - 5mm [color="Yellow (595nm)" package="5 mm [THT]"]
  R10 = Resistor [tolerance=±5% resistance=220 package=THT]
  LED5 = LED - 5mm [color="Red (660nm)" package="5 mm [THT]"]

nets:
  N1: S1.Pin_1, S1.Pin_2, R1.Pin_0
  N2: S1.Pin_3, S1.Pin_4, S2.Pin_3, S2.Pin_4, S3.Pin_3, S3.Pin_4, S4.Pin_3, S4.Pin_4, S5.Pin_3, S5.Pin_4, arduino_1.5V
  N3: S2.Pin_1, S2.Pin_2, R2.Pin_0
  N4: S3.Pin_1, S3.Pin_2, R3.Pin_0
  N5: S4.Pin_1, S4.Pin_2, R4.Pin_0
  N6: S5.Pin_1, S5.Pin_2, R5.Pin_0
  N7: arduino_1.D9_PWM, LED4.anode
  N8: arduino_1.D11_PWM/MOSI, LED5.anode
  N9: arduino_1.GND, R1.Pin_1, R2.Pin_1, R3.Pin_1, R4.Pin_1, R5.Pin_1, R6.Pin_1, R7.Pin_1, R8.Pin_1, R9.Pin_1, R10.Pin_1
  N10: arduino_1.D3_PWM, LED1.anode
  N11: arduino_1.D5_PWM, LED2.anode
  N12: arduino_1.D7, LED3.anode
  N13: LED1.cathode, R6.Pin_0
  N14: R7.Pin_0, LED2.cathode
  N15: R8.Pin_0, LED3.cathode
  N16: R9.Pin_0, LED4.cathode
  N17: R10.Pin_0, LED5.cathode
