# Fritzing sketch id1324_Demo_Board_005_0 (saved by Fritzing 0.9.3b)
circuit board: 6.88566cm x 5.36311cm
breadboards: 1

parts:
  Part1 = Arduino Uno (Rev3)
  D13 = LED - 5mm [color="Red (633nm)" package="5 mm [THT]"]
  D12 = LED - 5mm [color="Red (633nm)" package="5 mm [THT]"]
  D11~ = LED - 5mm [color="Red (633nm)" package="5 mm [THT]"]
  D10~ = LED - 5mm [color="Red (633nm)" package="5 mm [THT]"]
  D9~ = LED - 5mm [color="Red (633nm)" package="5 mm [THT]"]
  D8 = LED - 5mm [color="Red (633nm)" package="5 mm [THT]"]
  D7 = LED - 5mm [color="Red (633nm)" package="5 mm [THT]"]
  220_Ohm = Resistor [tolerance=±5% resistance=220 package=THT]
  220_Ohm_2 = Resistor [tolerance=±5% resistance=220 package=THT]
  220_Ohm_3 = Resistor [tolerance=±5% resistance=220 package=THT]
  S1 = Pushbutton [package=THT]  # not connected
  220_Ohm_4 = Resistor [tolerance=±5% resistance=220 package=THT]
  R6 = Resistor [tolerance=±5% resistance=220 package=THT]
  R7 = Resistor [tolerance=±5% resistance=220 package=THT]
  R8 = Resistor [tolerance=±5% resistance=220 package=THT]

nets:
  N1: Part1.D8, D8.anode
  N2: Part1.D9_PWM, D9~.anode
  N3: Part1.D10_PWM/SS, D10~.anode
  N4: Part1.D11_PWM/MOSI, D11~.anode
  N5: Part1.D12/MISO, D12.anode
  N6: Part1.D13/SCK, D13.anode
  N7: Part1.GND, 220_Ohm.Pin_0, 220_Ohm_2.Pin_0, 220_Ohm_3.Pin_0, 220_Ohm_4.Pin_0, R6.Pin_0, R7.Pin_0, R8.Pin_0
  N8: Part1.D7, D7.anode
  N9: D13.cathode, 220_Ohm_2.Pin_1
  N10: D12.cathode, 220_Ohm.Pin_1
  N11: D11~.cathode, 220_Ohm_3.Pin_1
  N12: D10~.cathode, 220_Ohm_4.Pin_1
  N13: D9~.cathode, R6.Pin_1
  N14: D8.cathode, R7.Pin_1
  N15: D7.cathode, R8.Pin_1
