# Fritzing sketch id1325_Demo_Board_008_0 (saved by Fritzing 0.9.3b)
circuit board: 6.88566cm x 5.36311cm
breadboards: 1

parts:
  Part1 = Arduino Uno (Rev3)
  D13 = LED - 5mm [color="Red (633nm)" package="5 mm [THT]"]
  D12 = LED - 5mm [color="Red (633nm)" package="5 mm [THT]"]
  D11~ = LED - 5mm [color="Red (633nm)" package="5 mm [THT]"]
  D10~ = LED - 5mm [color="Red (633nm)" package="5 mm [THT]"]
  D9~ = LED - 5mm [color="Red (633nm)" package="5 mm [THT]"]
  D8 = LED - 5mm [color="Red (633nm)" package="5 mm [THT]"]
  D7 = LED - 5mm [color="Red (633nm)" package="5 mm [THT]"]
  220R = Resistor [tolerance=±5% resistance=220 package=THT]
  220R_2 = Resistor [tolerance=±5% resistance=220 package=THT]
  220R_3 = Resistor [tolerance=±5% resistance=220 package=THT]
  S1 = Pushbutton [package=THT]
  220R_4 = Resistor [tolerance=±5% resistance=220 package=THT]
  220R_5 = Resistor [tolerance=±5% resistance=220 package=THT]
  220R_6 = Resistor [tolerance=±5% resistance=220 package=THT]
  220R_7 = Resistor [tolerance=±5% resistance=220 package=THT]
  Pot = Rotary Potentiometer (Small) [maximum_resistance=10kΩ package=THT]
  10KR = Resistor [tolerance=±5% resistance=10k package=THT]
  Reset_Sw = Momentary Switch [package=ksa_sealed_tac_switch]  # not connected
  SG1 = Buzzer 12mm [package=buzzer-ccv-kit]  # not connected
  LDR = PHOTOCELL [package=photocell-kit]  # not connected
  LED1 = LED - 3mm [color="Red (633nm)" package="3 mm [THT]"]
  560R = Resistor [tolerance=±5% resistance=220 package=THT]

nets:
  N1: Part1.A5/SCL, Pot.wiper
  N2: Part1.D8, D8.anode
  N3: Part1.D9_PWM, D9~.anode
  N4: Part1.D10_PWM/SS, D10~.anode
  N5: Part1.D11_PWM/MOSI, D11~.anode
  N6: Part1.D12/MISO, D12.anode
  N7: Part1.D13/SCK, D13.anode
  N8: Part1.GND, 220R.Pin_0, 220R_2.Pin_0, 220R_3.Pin_0, 220R_4.Pin_0, 220R_5.Pin_0, 220R_6.Pin_0, 220R_7.Pin_0, Pot.leg2, 10KR.Pin_1, LED1.cathode
  N9: Part1.D2, S1.leg0, 10KR.Pin_0
  N10: Part1.D7, D7.anode
  N11: Part1.5V, S1.leg1, Pot.leg1, 560R.Pin_1
  N12: D13.cathode, 220R_2.Pin_1
  N13: D12.cathode, 220R.Pin_1
  N14: D11~.cathode, 220R_3.Pin_1
  N15: D10~.cathode, 220R_4.Pin_1
  N16: D9~.cathode, 220R_5.Pin_1
  N17: D8.cathode, 220R_6.Pin_1
  N18: D7.cathode, 220R_7.Pin_1
  N19: LED1.anode, 560R.Pin_0
