# Fritzing sketch id1327_Demux_4051_0 (saved by Fritzing 0.7.10b)
breadboards: 1

parts:
  LED1 = LED - 5mm [color="Red (633nm)" package="5 mm [THT]"]
  LED2 = LED - 5mm [color="Red (633nm)" package="5 mm [THT]"]
  LED3 = LED - 5mm [color="Red (633nm)" package="5 mm [THT]"]
  LED4 = LED - 5mm [color="Red (633nm)" package="5 mm [THT]"]
  LED5 = LED - 5mm [color="Red (633nm)" package="5 mm [THT]"]
  LED6 = LED - 5mm [color="Red (633nm)" package="5 mm [THT]"]
  LED7 = LED - 5mm [color="Red (633nm)" package="5 mm [THT]"]
  LED8 = LED - 5mm [color="Red (633nm)" package="5 mm [THT]"]
  Arduino1 = Arduino
  R1 = Resistor [tolerance=±5% resistance=1k package=THT]
  R2 = Resistor [tolerance=±5% resistance=1k package=THT]
  R3 = Resistor [tolerance=±5% resistance=1k package=THT]
  R4 = Resistor [tolerance=±5% resistance=1k package=THT]
  R5 = Resistor [tolerance=±5% resistance=1k package=THT]
  R6 = Resistor [tolerance=±5% resistance=1k package=THT]
  R7 = Resistor [tolerance=±5% resistance=1k package=THT]
  R8 = Resistor [tolerance=±5% resistance=1k package=THT]
  IC1 = IC, DIP package, 16 pins [chip_label="IC 4051"]

nets:
  N1: LED1.cathode, LED2.cathode, LED3.cathode, LED4.cathode, LED5.cathode, LED6.cathode, LED7.cathode, LED8.cathode, Arduino1.GND, IC1.pin7, IC1.pin8
  N2: LED1.anode, R1.Pin_0
  N3: LED2.anode, R2.Pin_0
  N4: LED3.anode, R3.Pin_0
  N5: LED4.anode, R4.Pin_0
  N6: LED5.anode, R5.Pin_0
  N7: LED6.anode, R6.Pin_0
  N8: LED7.anode, R7.Pin_0
  N9: LED8.anode, R8.Pin_0
  N10: Arduino1.D3, IC1.pin10
  N11: Arduino1.D2, IC1.pin11
  N12: Arduino1.+5V, IC1.pin3, IC1.pin16
  N13: R1.Pin_1, IC1.pin13
  N14: R2.Pin_1, IC1.pin14
  N15: R3.Pin_1, IC1.pin15
  N16: R4.Pin_1, IC1.pin12
  N17: R5.Pin_1, IC1.pin1
  N18: R6.Pin_1, IC1.pin5
  N19: R7.Pin_1, IC1.pin2
  N20: R8.Pin_1, IC1.pin4

notes:
  [http://playground.arduino.cc/learning/4051
