# Fritzing sketch id1329_LED_0 (saved by Fritzing 0.9.3b)
breadboards: 1

parts:
  Part2 = Arduino Uno (Rev3)  # not connected
  Part3 = Arduino Motor Shield
  LED3 = RGB LED (com. cathode, rgb) [package="5 mm [THT]"]
  R1 = Resistor [tolerance=±5% resistance=330 package="0805 [SMD]"]
  R2 = Resistor [tolerance=±5% resistance=330 package="0805 [SMD]"]
  R3 = Resistor [tolerance=±5% resistance=330 package="0805 [SMD]"]
  S2 = Pushbutton [package="[THT]"]

nets:
  N1: Part3.GND, LED3.green_anode
  N2: LED3.red_anode, R1.Pin_0
  N3: LED3.common_cathode, R2.Pin_0
  N4: LED3.blue_anode, R3.Pin_0
  N5: S2.Pin_1, S2.Pin_2
  N6: S2.Pin_3, S2.Pin_4
