# Fritzing sketch id132_Raspberry_4ch_1_0 (saved by Fritzing 0.9.2b)
circuit board: 1.87805cm x 2.26018cm
breadboards: 1

parts:
  Q4 = NPN-Transistor [part_number=2N5550 package="TO92 [THT]"]
  Q1 = NPN-Transistor [part_number=2N5550 package="TO92 [THT]"]
  Q3 = NPN-Transistor [part_number=2N5550 package="TO92 [THT]"]
  Q2 = NPN-Transistor [part_number=2N5550 package="TO92 [THT]"]
  GND = female pin header, 1 pin [form="♀ (female)"]
  R4 = Resistor [tolerance=±5% resistance=150 package=THT]
  R1 = Resistor [tolerance=±5% resistance=150 package=THT]
  R3 = Resistor [tolerance=±5% resistance=150 package=THT]
  R2 = Resistor [tolerance=±5% resistance=150 package=THT]
  5V = female pin header, 1 pin [form="♀ (female)"]
  J2 = double row female pin header, 6 pins [form="♀ (female)"]
  J1 = female pin header, 6 pins [form="♀ (female)"]
  Raspberry_Pi2 = Raspberry Pi 2

nets:
  N1: Q4.E, Q1.E, Q3.E, Q2.E, GND.pin1, J2.pin4, J1.pin1, Raspberry_Pi2.GND
  N2: Q4.B, R4.Pin_0
  N3: Q4.C, J1.pin5
  N4: Q1.B, R1.Pin_0
  N5: Q1.C, J1.pin2
  N6: Q3.B, R3.Pin_0
  N7: Q3.C, J1.pin4
  N8: Q2.B, R2.Pin_1
  N9: Q2.C, J1.pin3
  N10: R4.Pin_1, J2.pin3, Raspberry_Pi2.GPIO21
  N11: R1.Pin_1, J2.pin6, Raspberry_Pi2.GPIO19
  N12: R3.Pin_1, J2.pin2, Raspberry_Pi2.GPIO20
  N13: R2.Pin_0, J2.pin5, Raspberry_Pi2.GPIO26
  N14: 5V.pin1, J1.pin6, Raspberry_Pi2.GPIO2, Raspberry_Pi2.5V
  N15: J2.pin1, Raspberry_Pi2.GPIO16

notes:
  R.W.
  Mokrator
  GPIO
  4x Relay
