# Fritzing sketch id1331_Color_detector_0 (saved by Fritzing 0.9.3b)
breadboards: 1

parts:
  Part1 = Arduino Uno (Rev3)
  LED1 = LED - 5mm [color="Green (555nm)" package="5 mm [THT]"]
  LED2 = LED - 5mm [color="Red (633nm)" package="5 mm [THT]"]
  LED3 = LED - 5mm [color="Yellow (595nm)" package="5 mm [THT]"]
  LED4 = LED - 5mm [color="Blue (430nm)" package="5 mm [THT]"]
  LED5 = LED - 5mm [color="Infrared (850nm)" package="5 mm [THT]"]
  R1 = Resistor [tolerance=±5% resistance=1k package=THT]
  R2 = Resistor [tolerance=±5% resistance=1k package=THT]
  R3 = Resistor [tolerance=±5% resistance=1k package=THT]
  R4 = Resistor [tolerance=±5% resistance=1k package=THT]
  R5 = Resistor [tolerance=±5% resistance=1k package=THT]
  CNY2 = CNY70
  R7 = Resistor [tolerance=±5% resistance=10k package=THT]
  R6 = Resistor [tolerance=±5% resistance=220 package=THT]

nets:
  N1: Part1.A0, CNY2.connector0, R7.Pin_1
  N2: Part1.GND, LED1.cathode, LED2.cathode, LED3.cathode, LED4.cathode, LED5.cathode, R7.Pin_0, R6.Pin_1
  N3: Part1.D2, R5.Pin_1
  N4: Part1.D3_PWM, R4.Pin_1
  N5: Part1.D4, R3.Pin_1
  N6: Part1.D5_PWM, R2.Pin_1
  N7: Part1.D6_PWM, R1.Pin_1
  N8: Part1.5V, CNY2.connector1, CNY2.connector2
  N9: LED1.anode, R1.Pin_0
  N10: LED2.anode, R2.Pin_0
  N11: LED3.anode, R3.Pin_0
  N12: LED4.anode, R4.Pin_0
  N13: LED5.anode, R5.Pin_0
  N14: CNY2.connector3, R6.Pin_0
