# Fritzing sketch id1334_Proyecto_con_ultrasonido_y_led_0 (saved by Fritzing 0.9.3b)
breadboards: 1

parts:
  hc-sr1 = hc-sr04
  Componente1 = Arduino Uno (Rev3)
  LED1 = LED - 5mm [color="Red (633nm)" package="5 mm [THT]"]
  R1 = Resistor [tolerance=±5% resistance=220 package="1206 [SMD]"]

nets:
  VCC: hc-sr1.VCC, Componente1.5V
  N1: hc-sr1.Trig, Componente1.D7
  N2: hc-sr1.Echo, Componente1.D6_PWM
  GND: hc-sr1.GND, Componente1.GND, R1.Pin_1
  N3: Componente1.D9_PWM, LED1.anode
  N4: LED1.cathode, R1.Pin_0

notes:
  Sensor ultrasonido HC-SR04
  Trig pulso de habilitación mide la distancia (naranja)
  Echo muestra el pulso proporcional al tiempo que tarda el sonido (amarillo)
  Detecta un objeto y se encienda la luz
