# Fritzing sketch id1336_proyecto_para_compartir_fritzing_0 (saved by Fritzing 0.9.3b)
breadboards: 1

parts:
  Componente1 = Arduino Uno (Rev3) - ICSP
  LED3 = LED - 5mm [color="Yellow (595nm)" package="5 mm [THT]"]
  LED4 = LED - 5mm [color="Red (633nm)" package="5 mm [THT]"]
  R1 = Resistor [tolerance=±5% resistance=220 package="2010 [SMD]"]
  R2 = Resistor [tolerance=±5% resistance=220 package="0805 [SMD]"]
  J1 = Piezo Speaker
  hc-sr1 = hc-sr04
  LED5 = LED - 5mm [color="Green (570nm)" package="5 mm [THT]"]
  R3 = Resistor [tolerance=±5% resistance=220 package="0805 [SMD]"]

nets:
  N1: Componente1.D10_PWM/SS, hc-sr1.Echo
  N2: Componente1.D11_PWM/MOSI, hc-sr1.Trig
  GND: Componente1.GND, LED3.cathode, LED4.cathode, J1.pin1, hc-sr1.GND, LED5.cathode
  N3: Componente1.D2, R3.Pin_1
  N4: Componente1.D3_PWM, R2.Pin_1
  N5: Componente1.D4, R1.Pin_1
  N6: Componente1.D5_PWM, J1.pin2
  5V: Componente1.5V, hc-sr1.VCC
  N7: LED3.anode, R2.Pin_0
  N8: LED4.anode, R1.Pin_0
  N9: LED5.anode, R3.Pin_0
