# Fritzing sketch id1337_Detector_de_ufos_0 (saved by Fritzing 0.7.11b)
breadboards: 1

parts:
  Arduino1 = Arduino
  R1 = Resistor [tolerance=±5% resistance=1M package=THT]
  R2 = Resistor [tolerance=±5% resistance=1M package=THT]
  R3 = Resistor [tolerance=±5% resistance=1M package=THT]
  R4 = Resistor [tolerance=±5% resistance=330 package=THT]
  VCC1 = Battery block 9V  # not connected
  J1 = Piezo Speaker
  R5 = Resistor [tolerance=±5% resistance=100 package=THT]
  LED1 = LED - 5mm [color="Blue (470nm)" package="5 mm [THT]"]
  LED2 = LED - 5mm [color="Yellow (585nm)" package="5 mm [THT]"]
  R6 = Resistor [tolerance=±5% resistance=100 package=THT]
  LED3 = LED - 5mm [color="Yellow (585nm)" package="5 mm [THT]"]
  LED4 = LED - 5mm [color="Green (560nm)" package="5 mm [THT]"]
  LED5 = LED - 5mm [color="Green (560nm)" package="5 mm [THT]"]
  R7 = Resistor [tolerance=±5% resistance=100 package=THT]
  R8 = Resistor [tolerance=±5% resistance=100 package=THT]
  R9 = Resistor [tolerance=±5% resistance=100 package=THT]
  R10 = Resistor [tolerance=±5% resistance=100 package=THT]

nets:
  N1: Arduino1.D7, R5.Pin_1
  N2: Arduino1.D6, LED1.anode, R6.Pin_0, R6.Pin_1
  N3: Arduino1.D5, LED2.anode, R7.Pin_0, R7.Pin_1
  N4: Arduino1.D4, LED3.anode, R8.Pin_0, R8.Pin_1
  N5: Arduino1.D3, LED4.anode, R9.Pin_0, R9.Pin_1
  N6: Arduino1.D2, LED5.anode, R10.Pin_0, R10.Pin_1
  N7: Arduino1.GND, R1.Pin_1, J1.pin1, LED1.cathode, LED2.cathode, LED3.cathode, LED4.cathode, LED5.cathode
  N8: Arduino1.A5, R4.Pin_0
  N9: R1.Pin_0, R2.Pin_1
  N10: R2.Pin_0, R3.Pin_1
  N11: R3.Pin_0, R4.Pin_1
  N12: J1.pin2, R5.Pin_0
