# Fritzing sketch id1339_servo_potentiomater_0 (saved by Fritzing 0.9.3b)
breadboards: 1

parts:
  パーツ1 = Arduino Uno (Rev3) - ICSP
  R1 = Trimmer Potentiometer [maximum_resistance=10kΩ package=THT]
  R2 = Trimmer Potentiometer [maximum_resistance=10kΩ package=THT]
  J1 = Basic Servo
  J2 = Basic Servo

nets:
  N1: パーツ1.A0, R1.wiper
  N2: パーツ1.A1, R2.wiper
  VCC: パーツ1.5V, R1.leg1, R2.leg1, J1.vcc, J2.vcc
  GND: パーツ1.GND, R1.leg2, R2.leg2, J1.gnd, J2.gnd
  N3: パーツ1.D9_PWM, J2.pulse
  N4: パーツ1.D10_PWM/SS, J1.pulse
