# Fritzing sketch id1341_luonnos_0 (saved by Fritzing 0.9.3b)
breadboards: 1

parts:
  Part1 = Bluetooth HC-05 Macho
  Part2 = Arduino Uno (Rev3)
  RHT1 = Humidity and Temperature Sensor RHT03

nets:
  N1: Part1.TXD, Part2.D10_PWM/SS
  N2: Part1.RXD, Part2.D11_PWM/MOSI
  VCC: Part1.VCC, Part2.5V, RHT1.Vcc
  GND: Part1.GND, Part2.GND, RHT1.GND_1
  N3: Part2.D2, RHT1.Data-signal
