# Fritzing sketch id1342_DHT11_LCD_0 (saved by Fritzing 0.9.2b)
breadboards: 1

parts:
  Part1 = Arduino Uno (Rev3)
  LCD1 = LCD screen
  DHT1 = DHT11_Temperature_and_Humitidy_Sensor
  U1 = POT [package=pot_mammoth]
  R1 = Resistor [tolerance=±5% resistance=220 package=THT]

nets:
  N1: Part1.D8, DHT1.connector2
  N2: Part1.D11_PWM/MOSI, LCD1.E
  N3: Part1.D12/MISO, LCD1.RS
  N4: Part1.D2, LCD1.DB7
  N5: Part1.D3_PWM, LCD1.DB6
  N6: Part1.D4, LCD1.DB5
  N7: Part1.D5_PWM, LCD1.DB4
  N8: Part1.5V, DHT1.connector1, U1.S, R1.Pin_0
  GND: Part1.GND, LCD1.VSS, LCD1.R/W, DHT1.connector4, U1.E
  N9: LCD1.VDD, R1.Pin_1
  N10: LCD1.V0, U1.A
