# Fritzing sketch id1343_Untitled_Sketch_0 (saved by Fritzing 0.9.3b)
breadboards: 1

parts:
  Part1 = Arduino Nano (Rev3.0)
  R1 = Trimmer Potentiometer [maximum_resistance=10kΩ package=THT]
  R2 = Photocell (LDR) [package=THT]
  R3 = Resistor [tolerance=±5% resistance=10k package=THT]
  R4 = Resistor [tolerance=±5% resistance=10k package=THT]
  RHT1 = Humidity and Temperature Sensor RHT03

nets:
  5V: Part1.5V, R1.leg1, R1.leg2, R4.Pin_1, RHT1.Vcc
  N1: R1.wiper, R2.pin_0
  N2: R2.pin_1, R3.Pin_0
  N3: R3.Pin_1, RHT1.GND_2
  N4: R4.Pin_0, RHT1.Data-signal
