# Fritzing sketch id1344_Heater_Control_DHT11_0 (saved by Fritzing 0.9.1b)
breadboards: 1

parts:
  U1 = RELAY [package=relay-t9a-2]
  Part1 = Arduino Nano (Rev3.0)
  DHT1 = prefix0010

nets:
  N1: U1.COIL1, Part1.GND, DHT1.connector11
  N2: U1.COIL2, Part1.D6
  N3: Part1.D5, DHT1.connector9
  N4: Part1.3V3, DHT1.connector8

notes:
  COM
  NC
  NO
  Note:
  The Relay is mounted on a PCB and therefore requires Vcc pin connected to 5v
