# Fritzing sketch id1345_DHT11_Esquema_0 (saved by Fritzing 0.9.2b)
breadboards: 1

parts:
  Parte1 = Arduino Uno (Rev3)
  DHT1 = DHT11_Temperature_and_Humitidy_Sensor

nets:
  N1: Parte1.D2, DHT1.connector2
  N2: Parte1.5V, DHT1.connector1
  N3: Parte1.GND, DHT1.connector4
