# Fritzing sketch id134_CarDuino_board_0 (saved by Fritzing 0.8.7b)
circuit board: 7.73989cm x 4.5cm

parts:
  IC1 = H-Bridge [package=THT]
  IC2 = H-Bridge [package=THT]
  J1 = female pin header, 2 pins [form="♀ (female)"]
  J3 = female pin header, 2 pins [form="♀ (female)"]
  J4 = female pin header, 2 pins [form="♀ (female)"]
  J2 = female pin header, 2 pins [form="♀ (female)"]
  Part1 = Arduino Pro Mini v13
  J6 = female pin header, 2 pins [form="♀ (female)"]
  R2 = Resistor [package="2010 [SMD]"]
  C1 = Ceramic Capacitor [capacitance="100 nF" package="1206 [SMD, multilayer]"]
  C2 = Ceramic Capacitor [capacitance="100 nF" package="1206 [SMD, multilayer]"]
  LED3 = LED - 5mm [color="Red (633nm)" package="5 mm [THT]"]
  J7 = female pin header, 3 pins [form="♀ (female)"]
  J8 = female pin header, 2 pins [form="♀ (female)"]
  U2 = Voltage Regulator - 5V [package="TO220 [THT]"]

nets:
  N1: IC1.1_2EN, IC2.1_2EN, Part1.D6_PWM
  N2: IC1.1A, Part1.D7
  N3: IC1.1Y, J2.pin2
  GND1: IC1.GND1, IC1.GND2, IC1.GND3, IC1.GND4, IC2.GND1, IC2.GND2, IC2.GND3, IC2.GND4, Part1.GND, J6.pin1, C1.0, C2.1, LED3.cathode, J7.pin1, U2.GND
  N4: IC1.2Y, J2.pin1
  N5: IC1.2A, Part1.D8
  N6: IC1.VCC2, IC1.VCC1, IC2.VCC2, IC2.VCC1, Part1.VCC, R2.Pin_0, C1.1, J7.pin2, U2.output_voltage
  N7: IC1.3_4EN, IC2.3_4EN, Part1.D9_PWM
  N8: IC1.3A, Part1.D12/MISO
  N9: IC1.3Y, J1.pin1
  N10: IC1.4Y, J1.pin2
  N11: IC1.4A, Part1.D13/SCK
  N12: IC2.1A, Part1.D2
  N13: IC2.1Y, J4.pin1
  N14: IC2.2Y, J4.pin2
  N15: IC2.2A, Part1.D3_PWM
  N16: IC2.3A, Part1.D4
  N17: IC2.3Y, J3.pin2
  N18: IC2.4Y, J3.pin1
  N19: IC2.4A, Part1.D5_PWM
  N20: Part1.D11_PWM/MOSI, J7.pin3
  N21: J6.pin2, J8.pin2
  N22: R2.Pin_1, LED3.anode
  N23: C2.0, J8.pin1, U2.input_voltage

notes:
  H Bridge
  5v  Pro Mini
  Switch
  Batt
  Data In
  M4
  M3
  M2
  M1
  LED
  REG
  Resistor
  CarDuino
