# Fritzing sketch id1355_DHT22_LCD_I2C_0 (saved by Fritzing 0.9.3b)
circuit board: 10.5759cm x 5.71717cm
breadboards: 1

parts:
  LCM1602_IIC1 = generic_ic_dip_22_300mil.fzp [part_number="LCM1602 IIC" chip_label="LCM1602 IIC"]
  LCD1 = LCD screen
  Part1 = Arduino Nano (Rev3.0)
  RHT1 = Humidity and Temperature Sensor RHT03 [part_number=DHT22]
  U2 = LIPO-1000mAh [package=lipo-1000]  # not connected

nets (from the pcb view):
  VSS: LCM1602_IIC1.connector0, LCM1602_IIC1.connector1, LCM1602_IIC1.connector2, LCM1602_IIC1.connector3, LCM1602_IIC1.connector5, LCM1602_IIC1.connector6, LCM1602_IIC1.connector7, LCM1602_IIC1.connector8, LCM1602_IIC1.connector9, LCM1602_IIC1.connector11, LCM1602_IIC1.connector12, LCM1602_IIC1.connector13, LCM1602_IIC1.connector14, LCM1602_IIC1.connector15, LCD1.VSS, LCD1.VDD, LCD1.V0, LCD1.RS, LCD1.E, LCD1.DB0, LCD1.DB1, LCD1.DB2, LCD1.DB3, LCD1.DB5, LCD1.DB6, LCD1.DB7, LCD1.LED+, LCD1.LED-
  N1: LCM1602_IIC1.connector4, LCD1.R/W
  N2: LCM1602_IIC1.connector10, LCD1.DB4
  N3: LCM1602_IIC1.connector16, Part1.GND, RHT1.GND_2
  N4: LCM1602_IIC1.connector17, Part1.5V
  N5: LCM1602_IIC1.connector18, Part1.A4
  N6: LCM1602_IIC1.connector19, Part1.A5
  N7: LCM1602_IIC1.connector20, LCM1602_IIC1.connector21
  N8: Part1.D9, RHT1.Data-signal
  3V3: Part1.3V3, RHT1.Vcc

notes:
  DHT22
