# Fritzing sketch id1356_DIAMEX_AVR_Tilduino_Adapter_0 (saved by Fritzing 0.7.1b)
perfboards: 1

parts:
  J1 = female pin header, 7 pins [form="♀ (female)"]
  J2 = male pin header, 2 pins [form="♂ (male)"]
  J3 = male pin header, 2 pins [form="♂ (male)"]
  J4 = male pin header, 2 pins [form="♂ (male)"]

nets:
  N1: J1.pin2, J3.pin2
  N2: J1.pin3, J2.pin1
  N3: J1.pin4, J3.pin1
  N4: J1.pin5, J2.pin2
  N5: J1.pin6, J4.pin1
  N6: J1.pin7, J4.pin2
