# Fritzing sketch id1357_dice_pcb_0 (saved by Fritzing 0.9.2b)
circuit board: 8.2293cm x 4.4925cm
breadboards: 1

parts:
  Part1 = Arduino Nano (Rev3.0)
  DI1 = 7-Segment LED Display [package=THT]
  S1 = Pushbutton [package="[THT]"]
  R1 = Resistor [tolerance=±5% resistance=220 package="1206 [SMD]"]

nets:
  N1: Part1.GND, DI1.commAnode, R1.Pin_0
  N2: Part1.D2, S1.Pin_1, S1.Pin_2
  N3: Part1.D3, DI1.cathodeG
  N4: Part1.D4, DI1.cathodeF
  N5: Part1.D5, DI1.cathodeA
  N6: Part1.D6, DI1.cathodeB
  N7: Part1.D8, DI1.cathodeE
  N8: Part1.D9, DI1.cathodeD
  N9: Part1.D10, DI1.cathodeC
  N10: Part1.5V, S1.Pin_3, S1.Pin_4
