# Fritzing sketch id1358_Dice3_smaller_0 (saved by Fritzing 0.9.0b)
circuit board: 4.10808cm x 3.75264cm
breadboards: 3

parts:
  U1 = 74HC595 [package="DIP16 [THT]"]
  R1 = Resistor [tolerance=±5% resistance=330 package=THT]
  R2 = Resistor [tolerance=±5% resistance=330 package=THT]
  R3 = Resistor [tolerance=±5% resistance=330 package=THT]
  R4 = Resistor [tolerance=±5% resistance=330 package=THT]
  R5 = Resistor [tolerance=±5% resistance=330 package=THT]
  R6 = Resistor [tolerance=±5% resistance=330 package=THT]
  R7 = Resistor [tolerance=±5% resistance=330 package=THT]
  LED1 = LED - 5mm [color="Red (633nm)" package="5 mm [THT]"]
  LED2 = LED - 5mm [color="Red (633nm)" package="5 mm [THT]"]
  LED3 = LED - 5mm [color="Red (633nm)" package="5 mm [THT]"]
  LED4 = LED - 5mm [color="Red (633nm)" package="5 mm [THT]"]
  LED5 = LED - 5mm [color="Red (633nm)" package="5 mm [THT]"]
  LED6 = LED - 5mm [color="Red (633nm)" package="5 mm [THT]"]
  LED7 = LED - 5mm [color="Red (633nm)" package="5 mm [THT]"]
  VCC1 = Battery
  S1 = Pushbutton [package="[THT]"]
  S2 = Toggle Switch [package=THT]
  R8 = Resistor [tolerance=±5% resistance=10k package=THT]
  IC1 = IC, DIP package, 8 pins [chip_label=ATTiny45]
  part = Resistor [tolerance=±5% resistance=220 package=THT]  # not connected

nets:
  N1: U1.Q1, R1.Pin_1
  N2: U1.Q2, R2.Pin_1
  N3: U1.Q3, R3.Pin_1
  N4: U1.Q4, R4.Pin_1
  N5: U1.Q5, R5.Pin_1
  N6: U1.Q6, R6.Pin_1
  N7: U1.Q7, R7.Pin_1
  GND: U1.GND, U1.OE, LED1.cathode, LED2.cathode, LED3.cathode, LED4.cathode, LED5.cathode, LED6.cathode, LED7.cathode, VCC1.-, S1.Pin_3, S1.Pin_4, IC1.pin4
  N8: U1.MR, U1.VCC, S2.L2, R8.Pin_0, IC1.pin8
  N9: U1.SH_CP, IC1.pin7
  N10: U1.ST_CP, IC1.pin6
  N11: U1.DS, IC1.pin2
  N12: R1.Pin_0, LED1.anode
  N13: R2.Pin_0, LED2.anode
  N14: R3.Pin_0, LED3.anode
  N15: R4.Pin_0, LED4.anode
  N16: R5.Pin_0, LED5.anode
  N17: R6.Pin_0, LED6.anode
  N18: R7.Pin_0, LED7.anode
  N19: VCC1.+, S2.COM
  N20: S1.Pin_1, S1.Pin_2, R8.Pin_1, IC1.pin3
