# Fritzing sketch id1359_Die_dumme_Arduino_Schaltung_0 (saved by Fritzing 0.9.2b)
breadboards: 1

parts:
  Bauteil1 = Arduino Uno (Rev3)
  Bauteil2 = Intel Galileo  # not connected
  Bauteil3 = Arduino Yun  # not connected
  Bauteil4 = Arduino BT  # not connected
  Bauteil5 = Arduino Mega 2560 (Rev3)  # not connected
  Bauteil6 = Arduino Mega ADK (Rev3)  # not connected
  Bauteil7 = Arduino Due (Rev2b)  # not connected
  Bauteil8 = Arduino Nano (Rev3.0)  # not connected
  Bauteil9 = Arduino Board Ethernet  # not connected
  Bauteil10 = Arduino Board Ethernet  # not connected
  Bauteil11 = Arduino Esplora (Rev4)  # not connected
  Bauteil12 = Arduino Leonardo (Rev3b)  # not connected
  Bauteil13 = Arduino Pro Mini v13  # not connected
  Bauteil14 = Arduino Micro (Rev3)  # not connected
  Arduino1 = Arduino Mini (Rev5)  # not connected
  Bauteil15 = Arduino Pro
  Bauteil16 = Arduino Fio (Funnel I/O)  # not connected
  Bauteil17 = Arduino GSM Shield  # not connected
  Bauteil18 = Arduino Ethernet Shield (Rev3)  # not connected
  Bauteil19 = Arduino Motor Shield (Rev3)  # not connected
  Bauteil20 = Arduino Wireless SD Shield  # not connected
  Bauteil21 = Arduino Prototyping Shield  # not connected
  Bauteil22 = Arduino Xbee Libellium Shield  # not connected

nets:
  N1: Bauteil1.AREF, Bauteil15.3V3
