# Fritzing sketch id135_Optoisolator_x4_0 (saved by Fritzing 0.7.11b)
breadboards: 1

parts:
  6N137 = IC, DIP package, 8 pins [chip_label=IC1]
  6N137_2 = IC, DIP package, 8 pins [chip_label=IC2]
  6N137_3 = IC, DIP package, 8 pins [chip_label=IC34]
  6N137_4 = IC, DIP package, 8 pins [chip_label=IC]
  C1 = Ceramic Capacitor [capacitance=100nF package="200 mil [THT, multilayer]"]
  C2 = Ceramic Capacitor [capacitance=100nF package="200 mil [THT, multilayer]"]
  C3 = Ceramic Capacitor [capacitance=100nF package="200 mil [THT, multilayer]"]
  C4 = Ceramic Capacitor [capacitance=100nF package="200 mil [THT, multilayer]"]
  In1 = Screw terminal - 2 pins [package=THT]
  In2 = Screw terminal - 2 pins [package=THT]
  In3 = Screw terminal - 2 pins [package=THT]
  In4 = Screw terminal - 2 pins [package=THT]
  R1 = Resistor [tolerance=±5% resistance=220 package=THT]
  Out = male pin header, 4 pins [form="♂ (male)"]
  R2 = Resistor [tolerance=±5% resistance=220 package=THT]
  R3 = Resistor [tolerance=±5% resistance=220 package=THT]
  R4 = Resistor [tolerance=±5% resistance=220 package=THT]
  uC_Power = male pin header, 2 pins [form="♂ (male)"]

nets:
  N1: 6N137.pin2, R1.Pin_0
  N2: 6N137.pin3, In1.pin2
  GND: 6N137.pin5, 6N137_2.pin5, 6N137_3.pin5, 6N137_4.pin5, C1.1, C2.1, C3.1, C4.1, uC_Power.pin1
  N3: 6N137.pin6, Out.pin4
  N4: 6N137.pin8, 6N137_2.pin8, 6N137_3.pin8, 6N137_4.pin8, C1.0, C2.0, C3.0, C4.0, uC_Power.pin2
  N5: 6N137_2.pin2, R2.Pin_0
  N6: 6N137_2.pin3, In2.pin2
  N7: 6N137_2.pin6, Out.pin3
  N8: 6N137_3.pin2, R3.Pin_0
  N9: 6N137_3.pin3, In3.pin2
  N10: 6N137_3.pin6, Out.pin2
  N11: 6N137_4.pin2, R4.Pin_1
  N12: 6N137_4.pin3, In4.pin2
  N13: 6N137_4.pin6, Out.pin1
  N14: In1.pin1, R1.Pin_1
  N15: In2.pin1, R2.Pin_1
  N16: In3.pin1, R3.Pin_1
  N17: In4.pin1, R4.Pin_0

notes:
  +5V
  gnd
  1
  2
  3
  4
  -
  +
