# Fritzing sketch id1360_DIEGO_Sketch_0 (saved by Fritzing 0.9.3b)
breadboards: 1

parts:
  Componente1 = Arduino Mega ADK (Rev3)
  LED1 = LED - 5mm [color="Red (633nm)" package="5 mm [THT]"]
  LED2 = LED - 5mm [color="Blue (505nm)" package="5 mm [THT]"]
  R1 = Resistor [tolerance=±5% resistance=220 package=THT]
  R2 = Resistor [tolerance=±5% resistance=220 package=THT]

nets:
  N1: Componente1.D11_PWM, LED2.cathode
  N2: Componente1.RESET, R1.Pin_1, R2.Pin_1
  N3: LED1.anode, R1.Pin_0
  N4: LED2.anode, R2.Pin_0
