# Fritzing sketch id1361_joystick_sega_funcional_0 (saved by Fritzing 0.9.2b)
circuit board: 3.69652cm x 3.72474cm
breadboards: 1

parts:
  R1 = Resistor [tolerance=±5% resistance=220 package=THT]
  R3 = Resistor [tolerance=±5% resistance=220 package=THT]
  U1 = ATTINY45 [package=dip]
  J4 = female pin header, 4 pins [form="♀ (female)"]
  R11 = Resistor [tolerance=±5% resistance=220 package=THT]
  IC2 = IC, DIP package, 16 pins [chip_label=IC]
  R15 = Resistor [tolerance=±5% resistance=220 package=THT]
  R16 = Resistor [tolerance=±5% resistance=220 package=THT]
  R17 = Resistor [tolerance=±5% resistance=220 package=THT]
  R18 = Resistor [tolerance=±5% resistance=220 package=THT]
  R22 = Resistor [tolerance=±5% resistance=220 package=THT]
  R23 = Resistor [tolerance=±5% resistance=220 package=THT]
  R24 = Resistor [tolerance=±5% resistance=220 package=THT]
  J7 = female pin header, 1 pin [form="♀ (female)"]
  J8 = female pin header, 1 pin [form="♀ (female)"]
  J9 = female pin header, 1 pin [form="♀ (female)"]
  J10 = female pin header, 1 pin [form="♀ (female)"]
  J11 = female pin header, 1 pin [form="♀ (female)"]
  J12 = female pin header, 1 pin [form="♀ (female)"]
  J13 = female pin header, 1 pin [form="♀ (female)"]
  J6 = female pin header, 3 pins [form="♀ (female)"]
  R25 = Resistor [tolerance=±5% resistance=220 package=THT]
  R26 = Resistor [tolerance=±5% resistance=220 package=THT]

nets:
  N1: R1.Pin_0, R3.Pin_0, J4.pin2, R25.Pin_1
  N2: R1.Pin_1, U1.PB3(ADC3)
  N3: R3.Pin_1, U1.VCC, J4.pin1, IC2.pin16, R23.Pin_1, R24.Pin_1, J9.pin1
  N4: U1.PB5(NRES), IC2.pin3
  N5: U1.PB4(ADC2), R11.Pin_1
  N6: U1.GND, J4.pin4, IC2.pin8, R15.Pin_0, R16.Pin_0, R17.Pin_0, R18.Pin_0, R22.Pin_0, J7.pin1, R25.Pin_0, R26.Pin_0
  N7: U1.PB0(MOSI), J10.pin1
  N8: U1.PB1(MISO), IC2.pin9
  N9: U1.PB2(SCK_ADC1), IC2.pin10
  N10: J4.pin3, R11.Pin_0, R26.Pin_1
  N11: IC2.pin1, R15.Pin_1, J13.pin1
  N12: IC2.pin4, R16.Pin_1, J6.pin3
  N13: IC2.pin5, R22.Pin_1, J6.pin2
  N14: IC2.pin6, R18.Pin_1, J6.pin1
  N15: IC2.pin7, R17.Pin_1, J12.pin1
  N16: IC2.pin11, J11.pin1
  N17: IC2.pin13, R24.Pin_0
  N18: IC2.pin14, R23.Pin_0
  N19: IC2.pin15, J8.pin1
