# Fritzing sketch id1362_DigipotBasis_0 (saved by Fritzing 0.7.12b)
breadboards: 1

parts:
  RE1 = Rotary Encoder [package=THT]
  Max = Pushbutton [package="[THT]"]
  Min = Pushbutton [package="[THT]"]
  IC1 = generic_ic_dip_8_300mil.fzp
  +_|_0 = female pin header, 3 pins [form="♀ (female)"]
  C1 = Tantalum Capacitor [capacitance=1µF package="100 mil [THT, tantalum]"]

nets:
  N1: RE1.EncoderPinA, IC1.connector6
  N2: RE1.EncoderPinC, Max.Pin_3, Max.Pin_4, Min.Pin_1, Min.Pin_2, IC1.connector7, +_|_0.pin1, C1.-
  N3: RE1.EncoderPinB, IC1.connector5
  N4: Max.Pin_2, IC1.connector4
  N5: Min.Pin_3, Min.Pin_4, IC1.connector2
  N6: IC1.connector0, IC1.connector3, +_|_0.pin3, C1.+
  N7: IC1.connector1, +_|_0.pin2

notes:
  Digitale potmeter, Digitale potmeter met onder- en boven-grens instelling, 0.9
  VTS-Digipot
