# Fritzing sketch id1363_KeyboardLED_0 (saved by Fritzing 0.9.1b)
breadboards: 1

parts:
  Digispark1 = generic_sip_9_300mil.fzp
  J1 = Screw terminal - 2 pins [package=THT]
  IC1 = Voltage Regulator [package=78xxl]
  C1 = Electrolytic Capacitor [capacitance=0.1µF voltage=50V package="100 mil [THT, electrolytic]"]
  S1 = Pushbutton [package="[THT]"]
  C2 = Electrolytic Capacitor [capacitance=0.21µF voltage=50V package="100 mil [THT, electrolytic]"]
  LED1 = LEDs [package=fkit-led-1206]
  Q1 = NPN-Transistor [package="SOT-23 [SMD]"]
  R1 = 9K Resistor

nets:
  N1: Digispark1.connector1, J1.pin1, IC1.GND, C1.-, C2.-, Q1.1, R1.connector1
  N2: Digispark1.connector2, IC1.OUT, C2.+
  N3: Digispark1.connector3, Q1.0
  N4: Digispark1.connector8, S1.Pin_1, S1.Pin_2, S1.Pin_3, S1.Pin_4, R1.connector0
  N5: J1.pin2, IC1.IN, C1.+, LED1.C
  N6: LED1.A, Q1.2
