# Fritzing sketch id1367_DigitalLineSensor_0 (saved by Fritzing 0.9.2b)
breadboards: 1

parts:
  LED13 = LED - 5mm [color="Blue (430nm)" package="5 mm [THT]"]
  LED14 = LED - 3mm [color="Infrared (880nm)" package="3 mm [THT]"]
  U1 = LM393 [package=so08]
  R1 = Resistor [tolerance=±5% resistance=220 package=THT]
  R3 = TRIMPOT [package=3362u-2]
  R4 = Resistor [tolerance=±5% resistance=220 package=THT]

nets:
  N1: LED13.cathode, U1.G1_-IN, R4.Pin_1
  N2: LED13.anode, LED14.cathode, U1.G1_V-, R3.CW
  N3: LED14.anode, R1.Pin_1
  N4: U1.G1_+IN, R3.WIPER
  N5: U1.G1_V+, R1.Pin_0, R3.CCW, R4.Pin_0
