# Fritzing sketch id136_Sketch_0 (saved by Fritzing 0.9.2b)
breadboards: 1

parts:
  Part1 = Arduino Uno (Rev3)
  SW1 = DIP Switch 8 Position [package=dipswitch-08]
  R1 = Resistor [tolerance=±5% resistance=10k package=THT]
  LED1 = RGB LED (com. cathode, rgb) [package="5 mm [THT]"]
  R2 = Resistor [tolerance=±5% resistance=330 package=THT]
  R3 = Resistor [tolerance=±5% resistance=330 package=THT]
  R4 = Resistor [tolerance=±5% resistance=330 package=THT]
  R5 = Resistor [tolerance=±5% resistance=10k package=THT]
  LED2 = LED - 5mm [color="Red (633nm)" package="5 mm [THT]"]
  R6 = Resistor [tolerance=±5% resistance=330 package=THT]
  R7 = PHOTOCELL [package=photocell-kit]
  R8 = Resistor [tolerance=±5% resistance=10k package=THT]

nets:
  N1: Part1.A0, R7.P$2, R8.Pin_0
  N2: Part1.D8, R3.Pin_1
  N3: Part1.D9_PWM, R4.Pin_1
  N4: Part1.D10_PWM/SS, R2.Pin_1
  N5: Part1.D1/TX, SW1.13, R5.Pin_1
  N6: Part1.D2, SW1.12, R1.Pin_1
  N7: Part1.D3_PWM, LED2.anode
  N8: Part1.5V, SW1.4, SW1.5, LED1.common_cathode, R7.P$1
  N9: Part1.GND, R1.Pin_0, R5.Pin_0, R6.Pin_0, R8.Pin_1
  N10: LED1.red_anode, R2.Pin_0
  N11: LED1.green_anode, R4.Pin_0
  N12: LED1.blue_anode, R3.Pin_0
  N13: LED2.cathode, R6.Pin_1
