# Fritzing sketch id1370_measure_0 (saved by Fritzing 0.9.0b)
circuit board: 6.88566cm x 5.36311cm
breadboards: 2

parts:
  LCD1 = LCD screen
  R2 = Resistor [tolerance=±5% resistance=220 package=THT]
  Contrast1 = Rotary Potentiometer (Small) [maximum_resistance=100kΩ package=THT]
  Arduino1 = Arduino Uno (Rev3)
  Part1 = SRF05 Ultrasonic Rangefinder

nets:
  VSS: LCD1.VSS, LCD1.R/W, LCD1.LED-, Contrast1.leg1, Arduino1.GND, Part1.connector11
  VDD: LCD1.VDD, R2.Pin_1, Contrast1.leg2, Arduino1.5V, Part1.connector8
  N1: LCD1.V0, Contrast1.wiper
  N2: LCD1.RS, Arduino1.D12/MISO
  N3: LCD1.E, Arduino1.D11_PWM/MOSI
  N4: LCD1.DB4, Arduino1.D5_PWM
  N5: LCD1.DB5, Arduino1.D4
  N6: LCD1.DB6, Arduino1.D3_PWM
  N7: LCD1.DB7, Arduino1.D2
  N8: LCD1.LED+, R2.Pin_0
  N9: Arduino1.D8, Part1.connector9
  N10: Arduino1.D9_PWM, Part1.connector10

notes:
  Code and more on character LCDs at http://arduino.cc/en/Tutorial/LiquidCrystal
