# Fritzing sketch id1371_tachometer_schematic_0 (saved by Fritzing 0.9.0b)
breadboards: 1

parts:
  R(LCD) = Rotary Potentiometer (Small) [maximum_resistance=10kΩ package=THT]
  LCD1 = LCD screen
  Microcontroller1 = Arduino Uno (Rev3)
  R(RPM) = Rotary Potentiometer (Small) [maximum_resistance=10kΩ package=THT]
  R2 = Resistor [tolerance=±5% resistance=220 package=THT]
  D2 = Rectifier Diode [part_number=1N4148 package="300 mil [THT]"]
  Q2 = NPN-Transistor [part_number=P2N2222A package="TO92 [THT]"]
  M1 = DC Motor

nets:
  VDD: R(LCD).leg1, LCD1.VDD, LCD1.LED+, Microcontroller1.5V, R(RPM).leg2, D2.cathode, M1.pin_1
  N1: R(LCD).wiper, LCD1.V0
  VSS: R(LCD).leg2, LCD1.VSS, LCD1.R/W, LCD1.LED-, Microcontroller1.GND, R(RPM).leg1, Q2.C
  N2: LCD1.RS, Microcontroller1.D12/MISO
  N3: LCD1.E, Microcontroller1.D11_PWM/MOSI
  N4: LCD1.DB4, Microcontroller1.D5_PWM
  N5: LCD1.DB5, Microcontroller1.D4
  N6: LCD1.DB6, Microcontroller1.D3_PWM
  N7: LCD1.DB7, Microcontroller1.D2
  N8: Microcontroller1.A0, R(RPM).wiper
  N9: Microcontroller1.D9_PWM, R2.Pin_0
  N10: R2.Pin_1, Q2.B
  N11: D2.anode, Q2.E, M1.pin_2
