# Fritzing sketch id1372_DigitalTapeMeasure_0 (saved by Fritzing 0.8.7b)
breadboards: 1

parts:
  Componente1 = Arduino Uno (Rev3)
  LCD1 = LCD screen
  U1 = generic_sip_4_300mil.fzp [chip_label=IC]
  R1 = Rotary Potentiometer (Large) [maximum_resistance=100kΩ package=THT]

nets:
  N1: Componente1.D8, LCD1.E
  N2: Componente1.D9_PWM, LCD1.DB4
  N3: Componente1.D10_PWM/SS, LCD1.DB5
  N4: Componente1.D11_PWM/MOSI, LCD1.DB6
  N5: Componente1.D12/MISO, LCD1.DB7
  GND: Componente1.GND, LCD1.VSS, LCD1.R/W, LCD1.LED-, U1.connector3, R1.leg1
  N6: Componente1.D2, U1.connector1
  N7: Componente1.D3_PWM, U1.connector2
  N8: Componente1.D7, LCD1.RS
  5V: Componente1.5V, LCD1.VDD, LCD1.LED+, U1.connector0, R1.leg2
  N9: LCD1.V0, R1.wiper
