# Fritzing sketch id1373_temp_in_c_f_0 (saved by Fritzing 0.8.7b)
breadboards: 1

parts:
  T1 = LM35 Temperature Sensor [package="TO92 [THT]"]
  Part1 = Arduino Uno (Rev3)

nets:
  N1: T1.+Vs, Part1.5V
  N2: T1.Vout, Part1.A0
  GND: T1.GND, Part1.GND
