# Fritzing sketch id1374_thermometer_0 (saved by Fritzing 0.9.1b)
circuit board: 23.5595cm x 15.2437cm
breadboards: 1

parts:
  Part1 = Arduino Uno (Rev3)
  16x2_LCD_display = LCD screen
  P1 = Trimmer Potentiometer [maximum_resistance=10kΩ package=THT]
  BAT1 = BC9VPC [package=bc9vpc]
  TMP36 = TMP36 Temperature Sensor [package="TO92 [THT]"]

nets:
  N1: Part1.A0, TMP36.Vout
  N2: Part1.D11_PWM/MOSI, 16x2_LCD_display.E
  N3: Part1.D12/MISO, 16x2_LCD_display.RS
  N4: Part1.D2, 16x2_LCD_display.DB7
  N5: Part1.D3_PWM, 16x2_LCD_display.DB6
  N6: Part1.D4, 16x2_LCD_display.DB5
  N7: Part1.D5_PWM, 16x2_LCD_display.DB4
  N8: Part1.3V3, 16x2_LCD_display.LED+
  5V: Part1.5V, 16x2_LCD_display.VDD, P1.leg1, TMP36.+Vs
  GND: Part1.GND, 16x2_LCD_display.VSS, 16x2_LCD_display.R/W, 16x2_LCD_display.LED-, P1.leg2, BAT1.V-, TMP36.GND
  N9: Part1.VIN, BAT1.V+
  N10: 16x2_LCD_display.V0, P1.wiper
