# Fritzing sketch id1376_TMP36_+_LCD_gtlw8IA_0 (saved by Fritzing 0.9.3b)
breadboards: 1

parts:
  LCD1 = LCD screen
  Onderdeel1 = Arduino Uno (Rev3)
  R1 = Resistor [tolerance=±5% resistance=220 package=THT]
  U2 = TMP36 [package=to-92-kit]
  LCD2 = LCD screen  # not connected

nets:
  GND: LCD1.VSS, LCD1.V0, LCD1.R/W, LCD1.LED-, Onderdeel1.GND, U2.GND
  VDD: LCD1.VDD, Onderdeel1.5V, R1.Pin_1, U2.VCC
  N1: LCD1.RS, Onderdeel1.D12/MISO
  N2: LCD1.E, Onderdeel1.D11_PWM/MOSI
  N3: LCD1.DB4, Onderdeel1.D5_PWM
  N4: LCD1.DB5, Onderdeel1.D4
  N5: LCD1.DB6, Onderdeel1.D3_PWM
  N6: LCD1.DB7, Onderdeel1.D2
  N7: LCD1.LED+, R1.Pin_0
  N8: Onderdeel1.A0, U2.VOUT

notes:
  VSS -1
  VDD -2
  V0 -3
  RS -4
  R/W -5
  ES -6
  DB0 -7
  DB1 -8
  DB2 -9
  DB3 -10
  DB4 -11
  DB5 -12
  DB6 -13
  DB7 -14
  LED SPLY -15
  LED GND -16
  1 TO GROUND
  2 TO PLUS
  3 TO GROUND
  4 TO 12
  5 TO GROUND
  6 TO 11
  7
  8
  9
  10
  11 TO 5
  12 TO 4
  13 TO 3
  14 TO 2
  15 TO ->220Resistor-> TO PLUS
  16 TO GROUND
