# Fritzing sketch id1377_DigitalThermometer_0 (saved by Fritzing 0.8.3b)
breadboards: 1

parts:
  LCD1 = LCD screen
  Arduino1 = Arduino Uno (Rev3)
  DHT1 = DHT11_Temperature_and_Humitidy_Sensor
  R3 = Trimmer Potentiometer [maximum_resistance=10kΩ package=THT]
  R4 = Resistor [tolerance=±5% resistance=220 package=THT]

nets:
  VSS: LCD1.VSS, LCD1.R/W, LCD1.LED-, Arduino1.GND, DHT1.connector4, R3.leg1
  VDD: LCD1.VDD, Arduino1.5V, DHT1.connector1, R3.leg2, R4.Pin_0
  N1: LCD1.V0, R3.wiper
  N2: LCD1.RS, Arduino1.D12/MISO
  N3: LCD1.E, Arduino1.D11_PWM/MOSI
  N4: LCD1.DB4, Arduino1.D5_PWM
  N5: LCD1.DB5, Arduino1.D4
  N6: LCD1.DB6, Arduino1.D3_PWM
  N7: LCD1.DB7, Arduino1.D2
  N8: LCD1.LED+, R4.Pin_1
  N9: Arduino1.D8, DHT1.connector2
