# Fritzing sketch id1378_Trumpet_0 (saved by Fritzing 0.8.7b)
breadboards: 1

parts:
  part = Arduino Uno (Rev3)
  R1 = Resistor [tolerance=±5% resistance=10k package=THT]
  R2 = Resistor [tolerance=±5% resistance=10k package=THT]
  R3 = Resistor [tolerance=±5% resistance=10k package=THT]
  Volume = Rotary Potentiometer (Small) [maximum_resistance=10kΩ package=THT]
  part_2 = Loudspeaker
  S1 = Pushbutton [package=THT]
  Valve_1 = Pushbutton [package=THT]
  Valve_2 = Pushbutton [package=THT]
  Valve_3 = Pushbutton [package=THT]
  Octave_Slide_Pot = Slide Potentiometer [maximum_resistance=100kΩ]

nets:
  N1: part.A0, Octave_Slide_Pot.wiper
  N2: part.D9_PWM, part_2.pin2
  N3: part.GND, R1.Pin_1, R2.Pin_1, R3.Pin_1, Volume.leg2, Octave_Slide_Pot.leg2
  N4: part.D2, R3.Pin_0, Valve_3.leg0
  N5: part.D3_PWM, R2.Pin_0, Valve_2.leg0
  N6: part.D4, R1.Pin_0, Valve_1.leg0
  N7: part.5V, Valve_1.leg1, Valve_2.leg1, Valve_3.leg1, Octave_Slide_Pot.leg1
  N8: Volume.wiper, S1.leg0
  N9: part_2.pin1, S1.leg1
