# Fritzing sketch id1379_RF_RX_Lamp_0 (saved by Fritzing 0.9.0b)
breadboards: 1

parts:
  Part1 = Arduino Uno (Rev3)
  LED1 = smd LED [color="White (4500K)" package="0603 [SMD]"]
  LED2 = smd LED [color="Blue (470nm)" package="0603 [SMD]"]
  LED3 = smd LED [color="White (4500K)" package="0603 [SMD]"]
  LED5 = smd LED [color="White (4500K)" package="0603 [SMD]"]
  LED6 = smd LED [color="White (4500K)" package="0603 [SMD]"]

nets:
  N1: Part1.D13/SCK, LED1.anode, LED2.anode, LED3.anode, LED5.anode, LED6.anode
  N2: Part1.GND, LED1.cathode, LED2.cathode, LED3.cathode, LED5.cathode, LED6.cathode

notes:
  This is a generic RF_RX part. (update to come)
  The other half of this project works on 315.00Mhz
