# Fritzing sketch id1380_RF_TX_LED_Controll_0 (saved by Fritzing 0.9.0b)
circuit board: 8.46667cm x 5.64444cm
breadboards: 1

parts:
  Part2 = Arduino Nano (Rev3.0)
  LED1 = RGB LED (com. cathode, rgb) [package="5 mm [THT]"]
  LED2 = RGB LED (com. cathode, rgb) [package="5 mm [THT]"]
  LED3 = RGB LED (com. cathode, rgb) [package="5 mm [THT]"]
  LED4 = RGB LED (com. cathode, rgb) [package="5 mm [THT]"]
  R1 = Trimmer Potentiometer [maximum_resistance=10kΩ package=THT]
  U4 = CustomPart
  ANT1 = Antenna
  U5 = SWITCH-SPST-2 [package=switch-spst-vertical]

nets:
  N1: Part2.GND, LED1.common_cathode, LED2.common_cathode, LED3.common_cathode, LED4.common_cathode, U4.connector2
  N2: Part2.D12/MISO, U4.connector1
  5V: Part2.5V, Part2.3V3, U5.O
  N3: LED1.red_anode, LED4.red_anode
  N4: LED1.green_anode, LED4.green_anode
  N5: LED1.blue_anode, LED2.blue_anode, LED3.blue_anode, LED4.blue_anode, R1.wiper
  N6: LED2.red_anode, LED3.red_anode
  N7: LED2.green_anode, LED3.green_anode
  N8: R1.leg2, U4.connector3, U5.P
  N9: U4.connector0, ANT1.antenna_lead
