# Fritzing sketch id1381_Cylon_Circuit_0 (saved by Fritzing 0.9.2b)
breadboards: 1

parts:
  VCC1 = Battery
  R1 = Resistor [tolerance=±5% resistance=220 package=THT]
  S1 = Pushbutton [package="[THT]"]
  C1 = Electrolytic Capacitor [capacitance=47µF package="100 mil [THT, electrolytic]"]
  R2 = Resistor [tolerance=±5% resistance=330 package=THT]
  R3 = Resistor [tolerance=±5% resistance=330k package=THT]
  C2 = Electrolytic Capacitor [capacitance=0.1µF package="100 mil [THT, electrolytic]"]
  U1 = 555 Timer [package="SO8 [SMD]"]
  LED1 = LED - 5mm [color="Red (633nm)" package="5 mm [THT]"]
  R4 = Resistor [tolerance=±5% resistance=220 package=THT]
  IC1 = prefix4017 [chip_label="IC 4017"]
  LED7 = LED - 5mm [color="Red (633nm)" package="5 mm [THT]"]
  D7 = Rectifier Diode [part_number=1N4001 package="300 mil [THT]"]
  D8 = Rectifier Diode [part_number=1N4001 package="300 mil [THT]"]
  D9 = Rectifier Diode [part_number=1N4001 package="300 mil [THT]"]
  D10 = Rectifier Diode [part_number=1N4001 package="300 mil [THT]"]
  D11 = Rectifier Diode [part_number=1N4001 package="300 mil [THT]"]
  D12 = Rectifier Diode [part_number=1N4001 package="300 mil [THT]"]
  D13 = Rectifier Diode [part_number=1N4001 package="300 mil [THT]"]
  D14 = Rectifier Diode [part_number=1N4001 package="300 mil [THT]"]
  D15 = Rectifier Diode [part_number=1N4001 package="300 mil [THT]"]
  D16 = Rectifier Diode [part_number=1N4001 package="300 mil [THT]"]
  LED8 = LED - 5mm [color="Red (633nm)" package="5 mm [THT]"]
  LED9 = LED - 5mm [color="Red (633nm)" package="5 mm [THT]"]
  LED10 = LED - 5mm [color="Red (633nm)" package="5 mm [THT]"]
  LED11 = LED - 5mm [color="Red (633nm)" package="5 mm [THT]"]
  LED12 = LED - 5mm [color="Red (633nm)" package="5 mm [THT]"]
  R5 = Resistor [tolerance=±5% resistance=220 package=THT]

nets:
  N1: VCC1.-, C1.-, C2.-, U1.Pin_1, LED1.cathode, IC1.connector7, IC1.connector12, IC1.connector14, R5.Pin_0
  N2: VCC1.+, R1.Pin_0, U1.Pin_4, U1.Pin_8, IC1.connector15
  N3: R1.Pin_1, S1.Pin_1, S1.Pin_2
  N4: S1.Pin_3, S1.Pin_4, C1.+, R2.Pin_0
  N5: R2.Pin_1, R3.Pin_0, U1.Pin_7
  N6: R3.Pin_1, C2.+, U1.Pin_2, U1.Pin_6
  N7: U1.Pin_3, R4.Pin_0, IC1.connector13
  N8: LED1.anode, R4.Pin_1
  N9: IC1.connector0, D16.anode
  N10: IC1.connector1, D14.anode
  N11: IC1.connector2, D7.anode
  N12: IC1.connector3, D8.anode
  N13: IC1.connector4, D9.anode
  N14: IC1.connector5, D10.anode
  N15: IC1.connector6, D11.anode
  N16: IC1.connector8, D12.anode
  N17: IC1.connector9, D13.anode
  N18: IC1.connector10, D15.anode
  N19: LED7.cathode, LED8.cathode, LED9.cathode, LED10.cathode, LED11.cathode, LED12.cathode, R5.Pin_1
  N20: LED7.anode, D9.cathode
  N21: D7.cathode, D8.cathode, LED11.anode
  N22: D10.cathode, D16.cathode, LED8.anode
  N23: D11.cathode, D15.cathode, LED10.anode
  N24: D12.cathode, D13.cathode, LED9.anode
  N25: D14.cathode, LED12.anode
