# Fritzing sketch id1384_Dimmer_0 (saved by Fritzing 0.9.3b)
breadboards: 1

parts:
  D1 = Rectifier Diode [part_number=1N4001 package="Melf DO-213 AB [SMD]"]
  D2 = Rectifier Diode [part_number=1N4001 package="Melf DO-213 AB [SMD]"]
  IC1 = General purpose bipolar Timer [package=dil-08]
  U1 = POT [package=pot_mammoth]
  LED1 = LED - 5mm [color="Red (633nm)" package="5 mm [THT]"]
  Q1 = PNP-Transistor [package="TO92 [THT]"]
  C1 = Ceramic Capacitor [capacitance=100nF package="100 mil [THT, multilayer]"]
  R5 = Resistor [tolerance=±5% resistance=220 package="1206 [SMD]"]

nets:
  N1: D1.cathode, D2.anode, IC1.TRI, IC1.TRE, C1.1
  N2: D1.anode, U1.S
  N3: D2.cathode, U1.E
  GND: IC1.GND, Q1.E, C1.0
  N4: IC1.OUT, U1.A, R5.Pin_0
  5V: IC1._RES, IC1.VCC+, LED1.anode
  N5: LED1.cathode, Q1.C
  N6: Q1.B, R5.Pin_1
