# Fritzing sketch id1385_Dimmer_0 (saved by Fritzing 0.9.1b)
circuit board: 8.46667cm x 5.64444cm
breadboards: 1

parts:
  Parte1 = Arduino Uno (Rev3)
  LED1 = LED - 5mm [color="Red (633nm)" package="5 mm [THT]"]
  R1 = Resistor [tolerance=±5% resistance=330 package=THT]
  U1 = POT [package=pot_mammoth]

nets:
  N1: Parte1.A0, U1.A
  N2: Parte1.D3_PWM, LED1.anode
  N3: Parte1.5V, U1.S
  N4: Parte1.GND, R1.Pin_0, U1.E
  N5: LED1.cathode, R1.Pin_1
