# Fritzing sketch id1386_diodo_led_paralelo_0 (saved by Fritzing 0.8.7b)
breadboards: 1

parts:
  R1 = Resistor [tolerance=±5% resistance=220 package=THT]
  LED1 = LED - 5mm [color="Red (633nm)" package="5 mm [THT]"]
  VCC1 = Battery block 9V
  R3 = Resistor [tolerance=±5% resistance=220 package=THT]  # not connected
  LED2 = LED - 5mm [color="Red (633nm)" package="5 mm [THT]"]  # not connected

nets:
  N1: R1.Pin_0, VCC1.+
  N2: R1.Pin_1, LED1.anode
  N3: LED1.cathode, VCC1.-

notes:
  Circuito paralelo de dos resistencias y dos diodos led.
