# Fritzing sketch id1387_Untitled_Sketch_0 (saved by Fritzing 0.6.3b)
breadboards: 1

parts:
  Arduino1 = Arduino
  LED1 = LED - 5mm [color="Red (633nm)" package="5 mm [THT]"]
  LED2 = LED - 5mm [color="Red (633nm)" package="5 mm [THT]"]
  R1 = Resistor [tolerance=±5% resistance=220 package=THT]

nets:
  N1: Arduino1.GND, R1.Pin_1
  N2: Arduino1.D9, LED1.cathode
  N3: Arduino1.D8, LED2.cathode
  N4: LED1.anode, LED2.anode, R1.Pin_0
