# Fritzing sketch id1389_disassemble_555_0 (saved by Fritzing 0.9.0b)
breadboards: 1

parts:
  IC1 = IC, DIP package, 8 pins [chip_label=IC]
  IC2 = IC, DIP package, 8 pins [chip_label=IC]
  IC3 = IC, DIP package, 14 pins [chip_label=IC]
  R1 = Resistor [tolerance=±5% resistance=4.7k package=THT]
  R2 = Resistor [tolerance=±5% resistance=4.7k package=THT]
  R3 = Resistor [tolerance=±5% resistance=4.7k package=THT]
  Q1 = PNP-Transistor [package="TO92 [THT]"]
  LED1 = LED - 5mm [color="Red (633nm)" package="5 mm [THT]"]
  R4 = Resistor [tolerance=±5% resistance=220 package=THT]

nets:
  N1: IC1.pin3, R1.Pin_0, R2.Pin_1
  N2: IC1.pin4, IC2.pin4, IC3.pin7, Q1.C
  N3: IC1.pin6, IC3.pin1
  N4: IC1.pin7, IC2.pin7, IC3.pin14, R1.Pin_1, R3.Pin_0
  N5: IC2.pin2, R2.Pin_0, R3.Pin_1
  N6: IC2.pin6, IC3.pin13
  N7: IC3.pin2, IC3.pin11, LED1.anode
  N8: IC3.pin3, IC3.pin12, Q1.B
  N9: LED1.cathode, R4.Pin_0
