# Fritzing sketch id138_7Segment_0 (saved by Fritzing 0.9.3b)
breadboards: 1

parts:
  Parça1 = Arduino Uno (Rev3)
  R1 = Resistor [tolerance=±5% resistance=220 package=THT]
  7_Segment1 = 7 Segment Display
  R2 = Resistor [tolerance=±5% resistance=220 package=THT]
  R3 = Resistor [tolerance=±5% resistance=220 package=THT]
  R4 = Resistor [tolerance=±5% resistance=220 package=THT]
  R5 = Resistor [tolerance=±5% resistance=220 package=THT]
  R6 = Resistor [tolerance=±5% resistance=220 package=THT]
  R7 = Resistor [tolerance=±5% resistance=220 package=THT]

nets:
  N1: Parça1.D8, R7.Pin_0
  N2: Parça1.GND, R1.Pin_0, 7_Segment1.Segment_DP, 7_Segment1.Segment_C, 7_Segment1.common_cathode#8, 7_Segment1.Segment_B, 7_Segment1.Segment_A#10, R2.Pin_0, R3.Pin_0
  N3: Parça1.D2, R1.Pin_1
  N4: Parça1.D3_PWM, R2.Pin_1
  N5: Parça1.D4, R3.Pin_1
  N6: Parça1.D5_PWM, R4.Pin_0
  N7: Parça1.D6_PWM, R5.Pin_0
  N8: Parça1.D7, R6.Pin_0
  N9: 7_Segment1.Segment_A#1, 7_Segment1.Segment_F, 7_Segment1.common_cathode#3, 7_Segment1.Segment_E, 7_Segment1.Segment_D, R4.Pin_1, R5.Pin_1, R6.Pin_1, R7.Pin_1
