# Fritzing sketch id1391_Disco_0 (saved by Fritzing 0.9.2b)
circuit board: 14.9576cm x 6.086cm

parts:
  Arduino_Yun = Arduino Yun
  Mosfet_Blue_1 = Basic FET N-Channel [package="TO220 [THT]"]
  Mosfet_Blue_2 = Basic FET N-Channel [package="TO220 [THT]"]
  Mosfet_Blue_3 = Basic FET N-Channel [package="TO220 [THT]"]
  Mosfet_Green_1 = Basic FET N-Channel [package="TO220 [THT]"]
  Mosfet_Green_2 = Basic FET N-Channel [package="TO220 [THT]"]
  Mosfet_Green_3 = Basic FET N-Channel [package="TO220 [THT]"]
  Mosfet_Red_3 = Basic FET N-Channel [package="TO220 [THT]"]
  Mosfet_Red_1 = Basic FET N-Channel [package="TO220 [THT]"]
  Mosfet_Red_2 = Basic FET N-Channel [package="TO220 [THT]"]
  RGB_M1_1 = female pin header, 4 pins [form="♀ (female)"]
  RGB_M1_2 = female pin header, 4 pins [form="♀ (female)"]
  RGB_M1_3 = female pin header, 4 pins [form="♀ (female)"]
  RGB_M1_4 = female pin header, 4 pins [form="♀ (female)"]
  RGB_M1_5 = female pin header, 4 pins [form="♀ (female)"]
  RGB_M1_6 = female pin header, 4 pins [form="♀ (female)"]
  RGB_M2_4 = female pin header, 4 pins [form="♀ (female)"]
  RGB_M2_3 = female pin header, 4 pins [form="♀ (female)"]
  RGB_M2_5 = female pin header, 4 pins [form="♀ (female)"]
  RGB_M2_2 = female pin header, 4 pins [form="♀ (female)"]
  RGB_M2_1 = female pin header, 4 pins [form="♀ (female)"]
  RGB_M2_6 = female pin header, 4 pins [form="♀ (female)"]
  RGB_M3_6 = female pin header, 4 pins [form="♀ (female)"]
  RGB_M3_1 = female pin header, 4 pins [form="♀ (female)"]
  RGB_M3_2 = female pin header, 4 pins [form="♀ (female)"]
  RGB_M3_5 = female pin header, 4 pins [form="♀ (female)"]
  RGB_M3_3 = female pin header, 4 pins [form="♀ (female)"]
  RGB_M3_4 = female pin header, 4 pins [form="♀ (female)"]
  Power_Input_M1 = Power plug
  Power_Input_M2 = Power plug
  Power_Input_M3 = Power plug
  Mosfet_White_1 = Basic FET N-Channel [package="TO220 [THT]"]
  Power_Input_M4 = Power plug
  White_M4_1 = female pin header, 2 pins [form="♀ (female)"]
  White_M4_2 = female pin header, 2 pins [form="♀ (female)"]
  White_M4_3 = female pin header, 2 pins [form="♀ (female)"]
  White_M4_4 = female pin header, 2 pins [form="♀ (female)"]
  White_M4_5 = female pin header, 2 pins [form="♀ (female)"]

nets:
  GND: Arduino_Yun.GND, Mosfet_Blue_1.source, Mosfet_Blue_2.source, Mosfet_Blue_3.source, Mosfet_Green_1.source, Mosfet_Green_2.source, Mosfet_Green_3.source, Mosfet_Red_3.source, Mosfet_Red_1.source, Mosfet_Red_2.source, Power_Input_M1.GND, Power_Input_M2.GND, Power_Input_M3.GND, Mosfet_White_1.source, Power_Input_M4.GND
  N1: Arduino_Yun.D9_PWM, Mosfet_White_1.gate
  N2: Arduino_Yun.D3/SCL, Arduino_Yun.D3_PWM, Mosfet_Blue_1.gate, Mosfet_Blue_2.gate, Mosfet_Blue_3.gate
  N3: Arduino_Yun.D5_PWM, Mosfet_Green_1.gate, Mosfet_Green_2.gate, Mosfet_Green_3.gate
  N4: Arduino_Yun.D6_PWM, Mosfet_Red_3.gate, Mosfet_Red_1.gate, Mosfet_Red_2.gate
  N5: Mosfet_Blue_1.drain, RGB_M1_1.pin1, RGB_M1_2.pin1, RGB_M1_3.pin1, RGB_M1_4.pin1, RGB_M1_5.pin1, RGB_M1_6.pin1
  N6: Mosfet_Blue_2.drain, RGB_M2_4.pin1, RGB_M2_3.pin1, RGB_M2_5.pin1, RGB_M2_2.pin1, RGB_M2_1.pin1, RGB_M2_6.pin1
  N7: Mosfet_Blue_3.drain, RGB_M3_6.pin1, RGB_M3_1.pin1, RGB_M3_2.pin1, RGB_M3_5.pin1, RGB_M3_3.pin1, RGB_M3_4.pin1
  N8: Mosfet_Green_1.drain, RGB_M1_1.pin3, RGB_M1_2.pin3, RGB_M1_3.pin3, RGB_M1_4.pin3, RGB_M1_5.pin3, RGB_M1_6.pin3
  N9: Mosfet_Green_2.drain, RGB_M2_4.pin3, RGB_M2_3.pin3, RGB_M2_5.pin3, RGB_M2_2.pin3, RGB_M2_1.pin3, RGB_M2_6.pin3
  N10: Mosfet_Green_3.drain, RGB_M3_6.pin3, RGB_M3_1.pin3, RGB_M3_2.pin3, RGB_M3_5.pin3, RGB_M3_3.pin3, RGB_M3_4.pin3
  N11: Mosfet_Red_3.drain, RGB_M3_6.pin4, RGB_M3_1.pin4, RGB_M3_2.pin4, RGB_M3_5.pin4, RGB_M3_3.pin4, RGB_M3_4.pin4
  N12: Mosfet_Red_1.drain, RGB_M1_1.pin4, RGB_M1_2.pin4, RGB_M1_3.pin4, RGB_M1_4.pin4, RGB_M1_5.pin4, RGB_M1_6.pin4
  N13: Mosfet_Red_2.drain, RGB_M2_4.pin4, RGB_M2_3.pin4, RGB_M2_5.pin4, RGB_M2_2.pin4, RGB_M2_1.pin4, RGB_M2_6.pin4
  N14: RGB_M1_1.pin2, RGB_M1_2.pin2, RGB_M1_3.pin2, RGB_M1_4.pin2, RGB_M1_5.pin2, RGB_M1_6.pin2, Power_Input_M1.VCC
  N15: RGB_M2_4.pin2, RGB_M2_3.pin2, RGB_M2_5.pin2, RGB_M2_2.pin2, RGB_M2_1.pin2, RGB_M2_6.pin2, Power_Input_M2.VCC
  N16: RGB_M3_6.pin2, RGB_M3_1.pin2, RGB_M3_2.pin2, RGB_M3_5.pin2, RGB_M3_3.pin2, RGB_M3_4.pin2, Power_Input_M3.VCC
  N17: Mosfet_White_1.drain, White_M4_1.pin2, White_M4_2.pin2, White_M4_3.pin2, White_M4_4.pin2, White_M4_5.pin2
  N18: Power_Input_M4.VCC, White_M4_1.pin1, White_M4_2.pin1, White_M4_3.pin1, White_M4_4.pin1, White_M4_5.pin1
