# Fritzing sketch id1392_Untitled_Sketch__0 (saved by Fritzing 0.7.4b)
breadboards: 1

parts:
  IC1 = L293D [package=THT]
  J3 = female pin header, 2 pins [form="♀ (female)"]
  J4 = female pin header, 2 pins [form="♀ (female)"]
  J6 = Screw terminal - 2 pins [package=THT]
  J7 = Screw terminal - 2 pins [package=THT]
  J8 = female pin header, 2 pins [form="♀ (female)"]
  J9 = female pin header, 2 pins [form="♀ (female)"]
  Arduino1 = Arduino
  D1 = Rectifier Diode [part_number=1N4001 package="300 mil [THT]"]
  D2 = Rectifier Diode [part_number=1N4001 package="300 mil [THT]"]
  D3 = Rectifier Diode [part_number=1N4001 package="300 mil [THT]"]
  D4 = Rectifier Diode [part_number=1N4001 package="300 mil [THT]"]
  D5 = Rectifier Diode [part_number=1N4001 package="300 mil [THT]"]
  D6 = Rectifier Diode [part_number=1N4001 package="300 mil [THT]"]
  D7 = Rectifier Diode [part_number=1N4001 package="300 mil [THT]"]
  D8 = Rectifier Diode [part_number=1N4001 package="300 mil [THT]"]

nets:
  N1: IC1.Enable_1, Arduino1.D3
  N2: IC1.In_1, Arduino1.D4
  N3: IC1.Out_1_(_Controlled_by_Enable_1_), J7.pin2, D1.anode, D2.cathode
  N4: IC1.0V, J3.pin1, J3.pin2, Arduino1.GND, D2.anode, D4.anode, D6.anode, D8.anode
  N5: IC1.Out_2_(_Controlled_by_Enable_1_), J7.pin1, D3.anode, D4.cathode
  N6: IC1.In_2, Arduino1.D9
  N7: IC1.+Vmotor, D1.cathode, D3.cathode
  N8: IC1.Enable_2, Arduino1.D11
  N9: IC1.In_3, Arduino1.D10
  N10: IC1.Out_3_(_Controlled_by_Enable_2_), J6.pin1, D7.anode, D8.cathode
  N11: IC1.Out_4_(_Controlled_by_Enable_2_), J6.pin2, D5.anode, D6.cathode
  N12: IC1.In_4, Arduino1.D2
  N13: IC1.+V, J8.pin1, J8.pin2
  N14: J4.pin1, J4.pin2
  N15: J9.pin1, J9.pin2, Arduino1.+5V
  N16: D5.cathode, D7.cathode
