# Fritzing sketch id1394_4051_0 (saved by Fritzing 0.8.7b)
breadboards: 1

parts:
  Parte1 = Arduino Uno (Rev3)
  7_Segment1 = 7 Segment Display
  HEF1 = HEF4094 [package="DIP16 [THT]"]
  R1 = Resistor [tolerance=±5% resistance=220 package=THT]

nets:
  N1: Parte1.D8, HEF1.Q's
  N2: Parte1.D9_PWM, HEF1.Q8
  N3: Parte1.D7, HEF1.Qs
  5V: Parte1.5V, HEF1.CLOCK, HEF1.Vdd
  N4: Parte1.GND, R1.Pin_0
  N5: 7_Segment1.Segment_G, HEF1.Q5
  N6: 7_Segment1.Segment_F, HEF1.DATA
  N7: 7_Segment1.common_anode, HEF1.Q6, R1.Pin_1
  N8: 7_Segment1.Segment_E, HEF1.STROBE
  N9: 7_Segment1.Segment_DP, HEF1.Q2
  N10: 7_Segment1.Segment_C, HEF1.Q7
  N11: 7_Segment1.Segment_B, HEF1.Q1
  N12: 7_Segment1.Segment_A, HEF1.OE
  N13: HEF1.Q3, HEF1.Q4, HEF1.Vss
