# Fritzing sketch id1395_LCD_0 (saved by Fritzing 0.7.10b)
breadboards: 1

parts:
  LCD1 = LCD screen
  R1 = Trimmer Potentiometer [maximum_resistance=10kΩ package=THT]
  Arduino_Ethernet_Shield1 = Arduino Ethernet Shield

nets:
  VSS: LCD1.VSS, LCD1.R/W, R1.leg1, Arduino_Ethernet_Shield1.GND
  VDD: LCD1.VDD, R1.leg2, Arduino_Ethernet_Shield1.+5V
  N1: LCD1.V0, R1.wiper
  N2: LCD1.RS, Arduino_Ethernet_Shield1.D7
  N3: LCD1.E, Arduino_Ethernet_Shield1.D6
  N4: LCD1.DB6, Arduino_Ethernet_Shield1.D5
  N5: LCD1.DB7, Arduino_Ethernet_Shield1.SS
  N6: LCD1.LED+, Arduino_Ethernet_Shield1.D3
  N7: LCD1.LED-, Arduino_Ethernet_Shield1.D2
