# Fritzing sketch id1396_test7_pushbutton_nokia5110_potentiometer_0 (saved by Fritzing 0.8.7b)
breadboards: 1

parts:
  Part1 = Arduino Uno (Rev3)
  S1 = Pushbutton [package="[THT]"]
  Nokia_5110_LCD_Module2 = Nokia5110LCDModule
  R1 = Rotary Potentiometer (Small) [maximum_resistance=100kΩ package=THT]
  R2 = Resistor [tolerance=±5% resistance=10k package=THT]

nets:
  N1: Part1.A0, R1.wiper
  N2: Part1.D8, Nokia_5110_LCD_Module2.connector4
  N3: Part1.D9_PWM, Nokia_5110_LCD_Module2.connector3
  N4: Part1.D10_PWM/SS, Nokia_5110_LCD_Module2.connector2
  N5: Part1.D11_PWM/MOSI, Nokia_5110_LCD_Module2.connector1
  N6: Part1.D12/MISO, Nokia_5110_LCD_Module2.connector0
  N7: Part1.D2, S1.Pin_1, S1.Pin_2, R2.Pin_0
  N8: Part1.D7, Nokia_5110_LCD_Module2.connector5
  N9: Part1.5V, S1.Pin_3, S1.Pin_4, Nokia_5110_LCD_Module2.connector6
  N10: Part1.GND, Nokia_5110_LCD_Module2.connector7, R1.leg2, R2.Pin_1
