# Fritzing sketch id1397_Projecte_0 (saved by Fritzing 0.9.3b)
breadboards: 1

parts:
  Componente1 = Arduino Uno (Rev3)
  R1 = Resistor [tolerance=±5% resistance=220 package=THT]
  R2 = Resistor [tolerance=±5% resistance=220 package=THT]
  Q1 = NPN-Transistor [package="TO92 [THT]"]
  J1 = Basic Servo
  M1 = DC Motor
  R3 = Resistor [tolerance=±5% resistance=220 package=THT]
  LED1 = smd LED [color="Red (633nm)" package="0805 [SMD]"]
  R4 = Photocell (LDR) [package=THT]
  R5 = Resistor [tolerance=±5% resistance=220 package=THT]

nets:
  N1: Componente1.A0, R4.pin_0, R5.Pin_0
  N2: Componente1.D9_PWM, J1.pulse
  N3: Componente1.D3_PWM, R2.Pin_1
  N4: Componente1.D4, R3.Pin_0
  N5: Componente1.3V3, R4.pin_1
  5V: Componente1.5V, R1.Pin_1, J1.vcc, M1.pin_1
  GND: Componente1.GND, Q1.C, J1.gnd, LED1.cathode, R5.Pin_1
  N6: R1.Pin_0, Q1.E, M1.pin_2
  N7: R2.Pin_0, Q1.B
  N8: R3.Pin_1, LED1.anode
