# Fritzing sketch id1399_Distance_Calculator_with_Arduino_and_LCD_Display_d1vQoKh_0 (saved by Fritzing 0.9.3b)
breadboards: 1

parts:
  Part1 = Arduino Uno (Rev3)
  hc-sr1 = hc-sr04
  LCD1 = LCD screen

nets:
  N1: Part1.D8, hc-sr1.Echo
  N2: Part1.D11_PWM/MOSI, LCD1.E
  N3: Part1.D12/MISO, LCD1.RS
  N4: Part1.D13/SCK, hc-sr1.Trig
  N5: Part1.D2, LCD1.DB7
  N6: Part1.D3_PWM, LCD1.DB6
  N7: Part1.D4, LCD1.DB5
  N8: Part1.D5_PWM, LCD1.DB4
  5V: Part1.5V, hc-sr1.VCC, LCD1.VDD
  GND: Part1.GND, hc-sr1.GND, LCD1.VSS, LCD1.V0, LCD1.R/W
