# Fritzing sketch id139_RPi_powerline_for_sensors___V1_0 (saved by Fritzing 0.9.2b)
stripboards: 1

parts:
  LED1 = LED - 5mm [color="Red (633nm)" package="5 mm [THT]"]
  J1 = Screw terminal - 2 pins [package=THT]
  S1 = Pushbutton [package=THT]
  R2 = Resistor [tolerance=±5% resistance=220 package=THT]
  U1 = Voltage Regulator - 5V [package="TO220 [THT]"]
  C2 = Ceramic Capacitor [capacitance=100nF package="100 mil [THT, multilayer]"]

nets:
  N1: LED1.cathode, J1.pin1, U1.GND
  N2: LED1.anode, R2.Pin_0
  N3: J1.pin2, S1.leg1
  N4: S1.leg0, C2.1
  N5: R2.Pin_1, U1.output_voltage
  N6: U1.input_voltage, C2.0

notes:
  5V
  GND
  220 Ohm
  3,3V
