# Fritzing sketch id1401_Ultrasonic_Distance_Finder_and_LCD_Screen_0 (saved by Fritzing 0.9.3b)
breadboards: 1

parts:
  HC-SR04_Sensor_1 = HC-SR04 Ultrasonic Distance Sensor
  Raspberry_Pi_1 = Raspberry Pi 3 [part_number=RPI-3-V1.2]
  LCD1 = LCD screen
  U1 = POT [package=pot_mammoth]
  U2 = POT [package=pot_mammoth]

nets:
  VCC: HC-SR04_Sensor_1.VCC, Raspberry_Pi_1.5V, LCD1.VDD, LCD1.LED-, U2.S
  N1: HC-SR04_Sensor_1.TRIG, Raspberry_Pi_1.GIPO23
  N2: HC-SR04_Sensor_1.ECHO, Raspberry_Pi_1.GIPO24
  GND: HC-SR04_Sensor_1.GND, Raspberry_Pi_1.GND, LCD1.VSS, LCD1.R/W, U1.E
  N3: Raspberry_Pi_1.GIPO11, LCD1.DB7
  N4: Raspberry_Pi_1.GIPO5, LCD1.DB6
  N5: Raspberry_Pi_1.GIPO6, LCD1.DB5
  N6: Raspberry_Pi_1.GIPO13, LCD1.DB4
  N7: Raspberry_Pi_1.GIPO19, LCD1.E
  N8: Raspberry_Pi_1.GIPO26, LCD1.RS
  N9: Raspberry_Pi_1.GIPO21, LCD1.DB0
  N10: Raspberry_Pi_1.GIPO20, LCD1.DB1
  N11: Raspberry_Pi_1.GIPO16, LCD1.DB2
  N12: Raspberry_Pi_1.GIPO12, LCD1.DB3
  N13: LCD1.V0, U1.A
  N14: LCD1.LED+, U2.A
