# Fritzing sketch id1402_distance_measurement_HC_SR04_0 (saved by Fritzing 0.9.3b)

parts:
  U1 = generic_sip_4_300mil.fzp [chip_label=IC]
  Componente1 = Arduino Uno (Rev3)

nets:
  N1: U1.connector0, Componente1.5V
  N2: U1.connector1, Componente1.D9_PWM
  N3: U1.connector2, Componente1.D8
  N4: U1.connector3, Componente1.GND
