# Fritzing sketch id1403_Ultrasonic_Range_Sensor_0 (saved by Fritzing 0.9.3b)
breadboards: 1

parts:
  Part1 = Arduino Uno (Rev3)
  hc-sr1 = hc-sr04
  LED1 = LED - 3mm [color="Orange (612nm)" package="3 mm [THT]"]
  LED2 = LED - 3mm [color="Orange (612nm)" package="3 mm [THT]"]
  LED3 = LED - 3mm [color="Green (560nm)" package="3 mm [THT]"]
  LED4 = LED - 3mm [color="Green (565nm)" package="3 mm [THT]"]
  LED5 = LED - 3mm [color="Red (633nm)" package="3 mm [THT]"]
  LED6 = LED - 3mm [color="Red (635nm)" package="3 mm [THT]"]
  R1 = Resistor [tolerance=±5% resistance=220 package="2010 [SMD]"]
  R2 = Resistor [tolerance=±5% resistance=220 package="2010 [SMD]"]
  R3 = Resistor [tolerance=±5% resistance=220 package="2010 [SMD]"]
  R4 = Resistor [tolerance=±5% resistance=220 package="2010 [SMD]"]
  R5 = Resistor [tolerance=±5% resistance=220 package="2010 [SMD]"]
  R6 = Resistor [tolerance=±5% resistance=220 package="2010 [SMD]"]

nets:
  N1: Part1.D9_PWM, hc-sr1.Trig
  N2: Part1.D10_PWM/SS, hc-sr1.Echo
  N3: Part1.D2, LED1.anode
  N4: Part1.D3_PWM, LED2.anode
  N5: Part1.D4, LED3.anode
  N6: Part1.D5_PWM, LED4.anode
  N7: Part1.D6_PWM, LED5.anode
  N8: Part1.D7, LED6.anode
  5V: Part1.5V, hc-sr1.VCC
  GND: Part1.GND, hc-sr1.GND, R1.Pin_0, R2.Pin_0, R3.Pin_0, R4.Pin_0, R5.Pin_0, R6.Pin_0
  N9: LED1.cathode, R1.Pin_1
  N10: LED2.cathode, R2.Pin_1
  N11: LED3.cathode, R4.Pin_1
  N12: LED4.cathode, R5.Pin_1
  N13: LED5.cathode, R6.Pin_1
  N14: LED6.cathode, R3.Pin_1
