# Fritzing sketch id1404_Distance_0 (saved by Fritzing 0.9.0b)
breadboards: 1

parts:
  J1 = Infrared Proximity Sensor
  パーツ1 = Arduino Uno (Rev3)
  neopixel1 = Neopixel_Ring_16

nets:
  N1: J1.Vout, パーツ1.A0
  GND: J1.GND, パーツ1.GND, neopixel1.connector1
  VCC: J1.Vcc, パーツ1.5V
  N2: パーツ1.D6_PWM, neopixel1.connector3
  N3: パーツ1.VIN, neopixel1.connector2

notes:
  近接センサーへの距離に応じてLEDが光ります。
