# Fritzing sketch id1405_FritzingDistMeasure_0 (saved by Fritzing 0.9.3b)
breadboards: 1

parts:
  Part8 = adafruit [part_number=938]  # not connected
  Part9 = adafruit [part_number="Adafruit #3316"]
  Part10 = Arduino Pro Mini v13

nets:
  N1: Part9.connector10, Part9.connector11, Part9.connector12
  N2: Part9.connector15, Part9.connector16
  N3: Part10.RAW, Part10.GND, Part10.RESET, Part10.D1/RX, Part10.D0/TX
  N4: Part10.A2, Part10.A1, Part10.A0, Part10.D13/SCK, Part10.D12/MISO
  N5: Part10.D7, Part10.D6_PWM, Part10.D5_PWM, Part10.D4, Part10.D3_PWM
