# Fritzing sketch id1406_DistanceWithLEDs_0 (saved by Fritzing 0.9.0b)
breadboards: 2

parts:
  Part1 = Arduino Uno (Rev3)
  LED3 = LED - 3mm [color="Green (555nm)" package="3 mm [THT]"]
  LED4 = LED - 3mm [color="Yellow (585nm)" package="3 mm [THT]"]
  LED5 = LED - 3mm [color="Red (633nm)" package="3 mm [THT]"]
  R3 = Resistor [tolerance=±5% resistance=330 package="0805 [SMD]"]
  R4 = Resistor [tolerance=±5% resistance=330 package="0805 [SMD]"]
  R5 = Resistor [tolerance=±5% resistance=330 package="0805 [SMD]"]
  Part2 = HC-SR04

nets:
  N1: Part1.D11_PWM/MOSI, Part2.connector10
  N2: Part1.D12/MISO, Part2.connector9
  N3: Part1.D2, LED3.anode
  N4: Part1.D3_PWM, LED4.anode
  N5: Part1.D4, LED5.anode
  N6: Part1.5V, Part2.connector8
  N7: Part1.GND, R3.Pin_0, R4.Pin_0, R5.Pin_0, Part2.connector11
  N8: LED3.cathode, R3.Pin_1
  N9: LED4.cathode, R4.Pin_1
  N10: LED5.cathode, R5.Pin_1
