# Fritzing sketch id1407_DIY_Arduino_0 (saved by Fritzing 0.4.3b)
breadboards: 1

parts:
  R1 = Resistor [resistance=220 package=THT]
  U1 = atmega168 [package="DIP28 [THT]"]
  C1 = Ceramic Capacitor [package=THT]
  C2 = Ceramic Capacitor [package=THT]
  XTAL1 = Crystal [package=THT]
  J1 = female pin header, 2 pins [form="♀ (female)"]
  J2 = female pin header, 2 pins [form="♀ (female)"]
  J3 = female pin header, 2 pins [form="♀ (female)"]
  J4 = female pin header, 2 pins [form="♀ (female)"]
  J5 = female pin header, 2 pins [form="♀ (female)"]
  J6 = female pin header, 2 pins [form="♀ (female)"]
  J7 = female pin header, 2 pins [form="♀ (female)"]
  J8 = female pin header, 2 pins [form="♀ (female)"]
  J9 = female pin header, 2 pins [form="♀ (female)"]
  J10 = female pin header, 2 pins [form="♀ (female)"]
  J11 = female pin header, 2 pins [form="♀ (female)"]
  J12 = female pin header, 2 pins [form="♀ (female)"]
  Power = Screw terminal - 2 pins [package=THT]

nets:
  N1: R1.Pin_0, U1.Pin_7, J7.pin1
  N2: R1.Pin_1, U1.Pin_1, J4.pin1
  N3: U1.Pin_2, J4.pin2
  N4: U1.Pin_3, J5.pin1
  N5: U1.Pin_4, J5.pin2
  N6: U1.Pin_5, J6.pin1
  N7: U1.Pin_6, J6.pin2
  N8: U1.Pin_8, U1.Pin_22, C1.pin_0, C2.pin_0, J7.pin2, Power.pin1
  N9: U1.Pin_9, C1.pin_1, XTAL1.pin_0
  N10: U1.Pin_10, C2.pin_1, XTAL1.pin_1
  N11: U1.Pin_11, J8.pin1
  N12: U1.Pin_12, J8.pin2
  N13: U1.Pin_13, J9.pin1
  N14: U1.Pin_14, J9.pin2
  N15: U1.Pin_15, J10.pin2
  N16: U1.Pin_16, J10.pin1
  N17: U1.Pin_17, J11.pin2
  N18: U1.Pin_18, J11.pin1
  N19: U1.Pin_19, J12.pin1, J12.pin2
  N20: U1.Pin_20, Power.pin2
  N21: U1.Pin_23, J3.pin2
  N22: U1.Pin_24, J3.pin1
  N23: U1.Pin_25, J2.pin2
  N24: U1.Pin_26, J2.pin1
  N25: U1.Pin_27, J1.pin2
  N26: U1.Pin_28, J1.pin1

notes:
  This is the representation of the example thought in http://mediascapes.net/wiki/index.php?title=DIY_Arduino
