# Fritzing sketch id1408_Arduino_Board_0 (saved by Fritzing 0.8.7b)
circuit board: 5.64444cm x 6.5cm
breadboards: 1

parts:
  ATMEGA_328 = IC, DIP package, 28 pins [chip_label=IC]
  16MHz_Crystal = Crystal [frequency="16 Mhz" package=THT]
  C1 = Ceramic Capacitor [capacitance=100nF package="100 mil [THT, multilayer]"]
  C2 = Ceramic Capacitor [capacitance=100nF package="100 mil [THT, multilayer]"]
  220 = Resistor [tolerance=±5% resistance=220 package=THT]
  LED = LED - 5mm [color="Red (633nm)" package="5 mm [THT]"]
  LM7805 = Voltage Regulator - 5V [package="TO220 [THT]"]
  9V_In = Battery block 9V
  S1 = Toggle Switch [package=THT]
  LED1 = LED - 5mm [color="Red (633nm)" package="5 mm [THT]"]
  220_2 = Resistor [tolerance=±5% resistance=220 package=THT]
  10k = Resistor [tolerance=±5% resistance=10k package=THT]

nets:
  N1: ATMEGA_328.pin1, 10k.Pin_0
  N2: ATMEGA_328.pin7, ATMEGA_328.pin20, ATMEGA_328.pin21, LM7805.output_voltage, 220_2.Pin_1, 10k.Pin_1
  N3: ATMEGA_328.pin8, ATMEGA_328.pin22, C1.0, C2.1, LED.anode, LM7805.GND, 9V_In.-, S1.COM, S1.L2, LED1.cathode
  N4: ATMEGA_328.pin9, 16MHz_Crystal.pin_0, C2.0
  N5: ATMEGA_328.pin10, 16MHz_Crystal.pin_1, C1.1
  N6: ATMEGA_328.pin19, 220.Pin_1
  N7: 220.Pin_0, LED.cathode
  N8: 9V_In.+, S1.L1
  N9: LED1.anode, 220_2.Pin_0

notes:
  +
  PWR
  Alex Willis
  Arduino Board
  developed with Fritzing
  Pin 13
