# Fritzing sketch id1409_ATtiny_Programmer_0 (saved by Fritzing 0.9.3b)
circuit board: 5.5cm x 7cm
breadboards: 1

parts:
  U1 = attiny85 [package=dip]
  Arduino_Uno = Arduino Uno (Rev3)
  J1 = female pin header, 4 pins [form="♀ (female)"]
  J2 = female pin header, 4 pins [form="♀ (female)"]
  C1 = Electrolytic Capacitor [capacitance=1µF package="200 mil [THT, electrolytic]"]

nets:
  N1: U1.Pin_1, Arduino_Uno.D10_PWM/SS, J2.pin1
  N2: U1.Pin_2, J2.pin2
  N3: U1.Pin_3, J2.pin3
  GND: U1.Pin_4, Arduino_Uno.GND, J2.pin4, C1.-
  11a: U1.Pin_5, Arduino_Uno.D11_PWM/MOSI, J1.pin4
  12b: U1.Pin_6, Arduino_Uno.D12/MISO, J1.pin3
  13c: U1.Pin_7, Arduino_Uno.D13/SCK, J1.pin2
  5V: U1.Pin_8, Arduino_Uno.5V, J1.pin1
  N4: Arduino_Uno.RESET, C1.+
