# Fritzing sketch id140_5ledbuzz_0 (saved by Fritzing 0.9.3b)
breadboards: 1

parts:
  Raspberry_Pi_1 = Raspberry Pi 3 [part_number=RPI-3-V1.2]
  R1 = Resistor [tolerance=±5% resistance=220 package=THT]
  R2 = Resistor [tolerance=±5% resistance=220 package=THT]
  R3 = Resistor [tolerance=±5% resistance=220 package=THT]
  R4 = Resistor [tolerance=±5% resistance=220 package=THT]
  R5 = Resistor [tolerance=±5% resistance=220 package=THT]
  LED1 = LED - 5mm [color="Green (555nm)" package="5 mm [THT]"]
  LED2 = LED - 5mm [color="Green (555nm)" package="5 mm [THT]"]
  LED3 = LED - 5mm [color="Green (555nm)" package="5 mm [THT]"]
  LED4 = LED - 5mm [color="Green (555nm)" package="5 mm [THT]"]
  LED5 = LED - 5mm [color="Green (555nm)" package="5 mm [THT]"]
  S1 = Pushbutton [package="[THT]"]
  J1 = Piezo Speaker

nets:
  N1: Raspberry_Pi_1.GPIO2, S1.Pin_3, S1.Pin_4
  N2: Raspberry_Pi_1.GPIO17, R1.Pin_0
  N3: Raspberry_Pi_1.GPIO27, R2.Pin_0
  N4: Raspberry_Pi_1.GPIO22, R3.Pin_0
  N5: Raspberry_Pi_1.GPIO10, R4.Pin_0
  N6: Raspberry_Pi_1.GPIO9, R5.Pin_0
  N7: Raspberry_Pi_1.GPIO14, J1.pin2
  N8: Raspberry_Pi_1.GND, LED1.anode, LED2.anode, LED3.anode, LED4.anode, LED5.anode, S1.Pin_1, S1.Pin_2, J1.pin1
  N9: R1.Pin_1, LED1.cathode
  N10: R2.Pin_1, LED2.cathode
  N11: R3.Pin_1, LED3.cathode
  N12: R4.Pin_1, LED4.cathode
  N13: R5.Pin_1, LED5.cathode
