# Fritzing sketch id1410_7_seg_Radio_0 (saved by Fritzing 0.8.7b)

parts:
  7_Segment2 = 7 Segment Display
  7_Segment13 = 7 Segment Display
  7_Segment22 = 7 Segment Display
  7_Segment23 = 7 Segment Display
  7_Segment24 = 7 Segment Display
  7_Segment25 = 7 Segment Display
  7_Segment26 = 7 Segment Display
  7_Segment27 = 7 Segment Display
  7_Segment28 = 7 Segment Display
  7_Segment29 = 7 Segment Display
  7_Segment30 = 7 Segment Display
  7_Segment31 = 7 Segment Display
  7_Segment33 = 7 Segment Display
  7_Segment34 = 7 Segment Display
  7_Segment35 = 7 Segment Display
  7_Segment36 = 7 Segment Display
  7_Segment37 = 7 Segment Display
  7_Segment38 = 7 Segment Display
  7_Segment39 = 7 Segment Display
  7_Segment40 = 7 Segment Display
  R1 = Resistor [tolerance=±5% resistance=220 package=THT]
  R2 = Resistor [tolerance=±5% resistance=220 package=THT]
  R3 = Resistor [tolerance=±5% resistance=220 package=THT]
  R4 = Resistor [tolerance=±5% resistance=220 package=THT]
  R5 = Resistor [tolerance=±5% resistance=220 package=THT]
  R6 = Resistor [tolerance=±5% resistance=220 package=THT]
  R7 = Resistor [tolerance=±5% resistance=220 package=THT]
  R8 = Resistor [tolerance=±5% resistance=220 package=THT]
  R9 = Resistor [tolerance=±5% resistance=220 package=THT]
  R10 = Resistor [tolerance=±5% resistance=220 package=THT]
  R11 = Resistor [tolerance=±5% resistance=220 package=THT]
  R12 = Resistor [tolerance=±5% resistance=220 package=THT]
  R13 = Resistor [tolerance=±5% resistance=220 package=THT]
  R14 = Resistor [tolerance=±5% resistance=220 package=THT]
  R15 = Resistor [tolerance=±5% resistance=220 package=THT]
  Com1_Swap_Freq = Pushbutton [package="[THT]"]
  Com1_MHz = Rotary Encoder [package=THT]
  Com1_KHz = Rotary Encoder [package=THT]
  Nav1_MHz = Rotary Encoder [package=THT]
  Nav1_KHz = Rotary Encoder [package=THT]
  Nav1_Swap_Freq = Pushbutton [package="[THT]"]
  R16 = Resistor [tolerance=±5% resistance=1k package=THT]
  R17 = Resistor [tolerance=±5% resistance=1k package=THT]
  Part1 = Arduino Mega 2560 (Rev3)

nets:
  N1: 7_Segment2.Segment_A, 7_Segment13.Segment_A, 7_Segment23.Segment_A, 7_Segment24.Segment_A, 7_Segment25.Segment_A, 7_Segment26.Segment_A, 7_Segment27.Segment_A, 7_Segment28.Segment_A, 7_Segment29.Segment_A, 7_Segment30.Segment_A, R15.Pin_1
  N2: 7_Segment2.Segment_F, 7_Segment13.Segment_F, 7_Segment23.Segment_F, 7_Segment24.Segment_F, 7_Segment25.Segment_F, 7_Segment26.Segment_F, 7_Segment27.Segment_F, 7_Segment28.Segment_F, 7_Segment29.Segment_F, 7_Segment30.Segment_F, R11.Pin_1
  N3: 7_Segment2.Segment_E, 7_Segment13.Segment_E, 7_Segment23.Segment_E, 7_Segment24.Segment_E, 7_Segment25.Segment_E, 7_Segment26.Segment_E, 7_Segment27.Segment_E, 7_Segment28.Segment_E, 7_Segment29.Segment_E, 7_Segment30.Segment_E, R9.Pin_1
  N4: 7_Segment2.Segment_D, 7_Segment13.Segment_D, 7_Segment23.Segment_D, 7_Segment24.Segment_D, 7_Segment25.Segment_D, 7_Segment26.Segment_D, 7_Segment27.Segment_D, 7_Segment28.Segment_D, 7_Segment29.Segment_D, 7_Segment30.Segment_D, R12.Pin_1
  N5: 7_Segment2.common_cathode#11, Part1.D28
  N6: 7_Segment2.common_cathode#12, 7_Segment13.common_cathode#12, 7_Segment23.common_cathode#12, 7_Segment24.common_cathode#12, 7_Segment25.common_cathode#12, 7_Segment26.common_cathode#12, 7_Segment27.common_cathode#12, 7_Segment28.common_cathode#12, 7_Segment29.common_cathode#12, 7_Segment30.common_cathode#12, R13.Pin_1
  N7: 7_Segment2.Segment_G, 7_Segment13.Segment_G, 7_Segment23.Segment_G, 7_Segment24.Segment_G, 7_Segment25.Segment_G, 7_Segment26.Segment_G, 7_Segment27.Segment_G, 7_Segment28.Segment_G, 7_Segment29.Segment_G, 7_Segment30.Segment_G, R10.Pin_1
  N8: 7_Segment2.Segment_B, 7_Segment13.Segment_B, 7_Segment23.Segment_B, 7_Segment24.Segment_B, 7_Segment25.Segment_B, 7_Segment26.Segment_B, 7_Segment27.Segment_B, 7_Segment28.Segment_B, 7_Segment29.Segment_B, 7_Segment30.Segment_B, R14.Pin_1
  N9: 7_Segment13.common_cathode#11, Part1.D27
  N10: 7_Segment22.Segment_A, 7_Segment31.Segment_A, 7_Segment33.Segment_A, 7_Segment34.Segment_A, 7_Segment35.Segment_A, 7_Segment36.Segment_A, 7_Segment37.Segment_A, 7_Segment38.Segment_A, 7_Segment39.Segment_A, 7_Segment40.Segment_A, R2.Pin_1
  N11: 7_Segment22.Segment_F, 7_Segment31.Segment_F, 7_Segment33.Segment_F, 7_Segment34.Segment_F, 7_Segment35.Segment_F, 7_Segment36.Segment_F, 7_Segment37.Segment_F, 7_Segment38.Segment_F, 7_Segment39.Segment_F, 7_Segment40.Segment_F, R6.Pin_1
  N12: 7_Segment22.Segment_E, 7_Segment31.Segment_E, 7_Segment33.Segment_E, 7_Segment34.Segment_E, 7_Segment35.Segment_E, 7_Segment35.common_cathode#5, 7_Segment35.common_cathode#11, 7_Segment36.Segment_E, 7_Segment37.Segment_E, 7_Segment38.Segment_E, 7_Segment39.Segment_E, 7_Segment40.Segment_E, R5.Pin_1, Part1.D42
  N13: 7_Segment22.Segment_DP, 7_Segment23.Segment_DP, 7_Segment28.Segment_DP, 7_Segment38.Segment_DP, R8.Pin_1
  N14: 7_Segment22.Segment_D, 7_Segment31.Segment_D, 7_Segment33.Segment_D, 7_Segment34.Segment_D, 7_Segment35.Segment_D, 7_Segment36.Segment_D, 7_Segment37.Segment_D, 7_Segment38.Segment_D, 7_Segment39.Segment_D, 7_Segment40.Segment_D, R4.Pin_1
  N15: 7_Segment22.common_cathode#11, Part1.D41
  N16: 7_Segment22.common_cathode#12, 7_Segment31.common_cathode#12, 7_Segment33.common_cathode#12, 7_Segment34.common_cathode#12, 7_Segment35.common_cathode#12, 7_Segment36.common_cathode#12, 7_Segment37.common_cathode#12, 7_Segment38.common_cathode#12, 7_Segment39.common_cathode#12, 7_Segment40.common_cathode#12, R3.Pin_1
  N17: 7_Segment22.Segment_G, 7_Segment31.Segment_G, 7_Segment33.Segment_G, 7_Segment34.Segment_G, 7_Segment35.Segment_G, 7_Segment36.Segment_G, 7_Segment37.Segment_G, 7_Segment38.Segment_G, 7_Segment39.Segment_G, 7_Segment40.Segment_G, R7.Pin_1
  N18: 7_Segment22.Segment_B, 7_Segment31.Segment_B, 7_Segment33.Segment_B, 7_Segment34.Segment_B, 7_Segment35.Segment_B, 7_Segment36.Segment_B, 7_Segment37.Segment_B, 7_Segment38.Segment_B, 7_Segment39.Segment_B, 7_Segment40.Segment_B, R1.Pin_1
  N19: 7_Segment23.common_cathode#11, Part1.D29
  N20: 7_Segment24.common_cathode#11, Part1.D30
  N21: 7_Segment25.common_cathode#11, Part1.D31
  N22: 7_Segment26.common_cathode#11, Part1.D22
  N23: 7_Segment27.common_cathode#11, Part1.D23
  N24: 7_Segment28.common_cathode#11, Part1.D24
  N25: 7_Segment29.common_cathode#11, Part1.D25
  N26: 7_Segment30.common_cathode#11, Part1.D26
  N27: 7_Segment31.common_cathode#11, Part1.D39
  N28: 7_Segment33.common_cathode#11, Part1.D44
  N29: 7_Segment34.common_cathode#11, Part1.D40
  N30: 7_Segment36.common_cathode#11, Part1.D43
  N31: 7_Segment37.common_cathode#11, Part1.D45
  N32: 7_Segment38.common_cathode#11, Part1.D46
  N33: 7_Segment39.common_cathode#11, Part1.D47
  N34: 7_Segment40.common_cathode#11, Part1.D48
  N35: R1.Pin_0, Part1.D33
  N36: R2.Pin_0, Part1.D32
  N37: R3.Pin_0, Part1.D34
  N38: R4.Pin_0, Part1.D35
  N39: R5.Pin_0, Part1.D36
  N40: R6.Pin_0, Part1.D37
  N41: R7.Pin_0, Part1.D38
  N42: R8.Pin_0, Com1_Swap_Freq.Pin_4, Nav1_Swap_Freq.Pin_4, Part1.5V
  N43: R9.Pin_0, Part1.D6_PWM
  N44: R11.Pin_0, Part1.D7_PWM
  N45: R12.Pin_0, Part1.D5_PWM
  N46: R13.Pin_0, Part1.D4_PWM
  N47: R14.Pin_0, Part1.D3_PWM
  N48: R15.Pin_0, Part1.D2_PWM
  N49: Com1_Swap_Freq.Pin_1, Com1_Swap_Freq.Pin_2, Part1.D18/TX1
  N50: Com1_MHz.EncoderPinA, Part1.D10_PWM
  N51: Com1_MHz.EncoderPinC, Com1_KHz.EncoderPinC, Nav1_MHz.EncoderPinC, Nav1_KHz.EncoderPinC, R16.Pin_1, R17.Pin_1, Part1.GND
  N52: Com1_MHz.EncoderPinB, Part1.D9_PWM
  N53: Com1_KHz.EncoderPinA, Part1.D12_PWM
  N54: Com1_KHz.EncoderPinB, Part1.D11_PWM
  N55: Nav1_MHz.EncoderPinA, Part1.D49
  N56: Nav1_MHz.EncoderPinB, Part1.D50
  N57: Nav1_KHz.EncoderPinA, Part1.D51
  N58: Nav1_KHz.EncoderPinB, Part1.D52
  N59: Nav1_Swap_Freq.Pin_1, Nav1_Swap_Freq.Pin_2, Part1.D19/RX1

notes:
  Com1 StandBy Display
  Com1 Active Display
  Nav 1 StandBy Display
  Nav 1 Active Display
  Com1 Rotary Encoders
  Nav1 Rotary Encoders
  Com1/ Nav1 Active/Standby Switch
