# Fritzing sketch id1412_buring_bootloader_0 (saved by Fritzing 0.9.2b)
breadboards: 1

parts:
  Part1 = Arduino Uno (Rev3) - ICSP
  U1 = atmega328 [package=dip]
  Y1 = CRYSTAL [package=hc49us]
  R1 = Resistor [tolerance=±5% resistance=10k package="1206 [SMD]"]
  R2 = Resistor [tolerance=±5% resistance=220 package="1206 [SMD]"]
  LED1 = LEDs [package=led10mm]

nets:
  N1: Part1.D0/RX, U1.D0_(RX)
  N2: Part1.D1/TX, U1.D1_(TX)
  N3: Part1.RESET, U1.RESET, R1.Pin_0
  N4: Part1.5V, R1.Pin_1
  N5: Part1.GND, R2.Pin_1
  N6: U1.XLAT1, Y1.1
  N7: U1.XLAT2, Y1.2
  N8: U1.D13, LED1.C
  N9: R2.Pin_0, LED1.A

notes:
  Remove IC
