# Fritzing sketch id1413_Light_Sensor_Bit_0 (saved by Fritzing 0.9.2b)
circuit board: 4.5cm x 4.5cm
breadboards: 1

parts:
  U1 = 555 Timer [package="DIP8 [THT]"]
  R1 = Resistor [tolerance=±5% resistance=10k package=THT]
  R2 = Resistor [tolerance=±5% resistance=22k package=THT]
  C1 = Ceramic Capacitor [capacitance=10nF package="100 mil [THT, multilayer]"]
  C2 = Ceramic Capacitor [capacitance=100nF package="100 mil [THT, multilayer]"]
  VCC1 = Battery block 9V
  LDR = Photocell (LDR) [package=THT]
  R4 = Resistor [tolerance=±5% resistance=1k package=THT]
  R5 = Rotary Potentiometer (Small) [maximum_resistance=100kΩ package=THT]
  U2 = mystery part, 3 pins [chip_label=?]

nets:
  N1: U1.Ground, C1.0, C2.0, VCC1.-, R5.leg1, R5.wiper, U2.pin1
  N2: U1.Trigger, U1.Threshold, R1.Pin_1, C2.1
  N3: U1.Output, U2.pin2
  N4: U1.Reset, LDR.pin_1, R4.Pin_0
  N5: U1.Control_Voltage, C1.1
  N6: U1.Discharge, R1.Pin_0, R2.Pin_1
  N7: U1.Vcc_Supply_Voltage, R2.Pin_0, VCC1.+, LDR.pin_0, U2.pin3
  N8: R4.Pin_1, R5.leg2
