# Fritzing sketch id1414_diy_shrimp_0 (saved by Fritzing 0.9.2b)
circuit board: 8.04359cm x 2.79991cm
breadboards: 1

parts:
  FTDI = female pin header, 6 pins [form="♀ (female)"]
  Power_plug1 = Power plug
  ATMEGA_8-88-168-328p = atmega168 [package=dip]
  J2 = female pin header, 4 pins [form="♀ (female)"]
  J3 = female pin header, 6 pins [form="♀ (female)"]
  J4 = female pin header, 14 pins [form="♀ (female)"]
  C1 = Ceramic Capacitor [capacitance=100nF package="100 mil [THT, multilayer]"]
  RESET = Pushbutton [package="[THT]"]
  C2 = Ceramic Capacitor [capacitance=0.1µF package="100 mil [THT, multilayer]"]
  R1 = Resistor [tolerance=±5% resistance=10k package=THT]
  7805 = Voltage Regulator - 5V [package="TO220 [THT]"]
  D1 = Rectifier Diode [part_number=1N4007 package="300 mil [THT]"]
  C3 = Electrolytic Capacitor [capacitance=47µF voltage=20V package="100 mil [THT, electrolytic]"]
  C4 = Electrolytic Capacitor [capacitance=47µF voltage=20V package="100 mil [THT, electrolytic]"]
  C5 = Ceramic Capacitor [capacitance=0.1µF package="100 mil [THT, multilayer]"]
  R2 = Resistor [tolerance=±5% resistance=220 package=THT]
  LED1 = LED - 5mm [color="Red (633nm)" package="5 mm [THT]"]
  ON/OFF = female pin header, 3 pins [form="♀ (female)"]
  XTAL1 = Crystal [frequency="16 Mhz" package=THT]
  C6 = Ceramic Capacitor [capacitance=28pF package="100 mil [THT, multilayer]"]
  C7 = Ceramic Capacitor [capacitance=28pF package="100 mil [THT, multilayer]"]

nets:
  GND: FTDI.pin1, FTDI.pin2, Power_plug1.GND, ATMEGA_8-88-168-328p.GND, J4.pin8, C1.1, RESET.Pin_1, RESET.Pin_2, 7805.GND, C3.-, C4.-, C5.0, LED1.anode, C6.1, C7.0
  N1: FTDI.pin3, ATMEGA_8-88-168-328p.VCC, ATMEGA_8-88-168-328p.AVCC, J4.pin6, R1.Pin_1, 7805.output_voltage, C4.+, C5.1, R2.Pin_1
  N2: FTDI.pin4, ATMEGA_8-88-168-328p.D1_(TX), J3.pin4
  N3: FTDI.pin5, ATMEGA_8-88-168-328p.D0_(RX), J3.pin5
  N4: FTDI.pin6, C2.1
  N5: Power_plug1.VCC, ON/OFF.pin1
  N6: ATMEGA_8-88-168-328p.RESET, J3.pin6, RESET.Pin_3, RESET.Pin_4, C2.0, R1.Pin_0
  N7: ATMEGA_8-88-168-328p.D2, J3.pin3
  N8: ATMEGA_8-88-168-328p.D3_(PWM), J3.pin2
  N9: ATMEGA_8-88-168-328p.D4, J3.pin1
  N10: ATMEGA_8-88-168-328p.XLAT1, XTAL1.pin_1, C6.0
  N11: ATMEGA_8-88-168-328p.XLAT2, XTAL1.pin_0, C7.1
  N12: ATMEGA_8-88-168-328p.D5_(PWM), J2.pin4
  N13: ATMEGA_8-88-168-328p.D6_(PWM), J2.pin3
  N14: ATMEGA_8-88-168-328p.D7, J2.pin2
  N15: ATMEGA_8-88-168-328p.D8, J2.pin1
  N16: ATMEGA_8-88-168-328p.D9_(PWM), J4.pin1
  N17: ATMEGA_8-88-168-328p.D10_(PWM), J4.pin2
  N18: ATMEGA_8-88-168-328p.D11_(PWM), J4.pin3
  N19: ATMEGA_8-88-168-328p.D12, J4.pin4
  N20: ATMEGA_8-88-168-328p.D13, J4.pin5
  N21: ATMEGA_8-88-168-328p.AREF, J4.pin7, C1.0
  N22: ATMEGA_8-88-168-328p.A0, J4.pin9
  N23: ATMEGA_8-88-168-328p.A1, J4.pin10
  N24: ATMEGA_8-88-168-328p.A2, J4.pin11
  N25: ATMEGA_8-88-168-328p.A3, J4.pin12
  N26: ATMEGA_8-88-168-328p.A4, J4.pin13
  N27: ATMEGA_8-88-168-328p.A5, J4.pin14
  N28: 7805.input_voltage, D1.cathode, C3.+
  N29: D1.anode, ON/OFF.pin2
  N30: R2.Pin_0, LED1.cathode
