# Fritzing sketch id1415_DIY_USB_charger_0 (saved by Fritzing 0.9.3b)

parts:
  LM1 = RioRand LM2596
  X1 = USB Connectors [package=usb-a-s-silk-female]
  BAT1 = BC9VPC [package=bc9vpc]

nets:
  N1: LM1.Pin_0, BAT1.V+
  N2: LM1.Pin_1, BAT1.V-
  N3: LM1.Pin_2, X1.D+
  N4: LM1.Pin_3, X1.GND
