# Fritzing sketch id1417_DJ_booth_0 (saved by Fritzing 0.9.2b)
circuit board: 8.57437cm x 7.87652cm
breadboards: 3

parts:
  Part1 = Arduino Nano (Rev3.0)
  C1 = Electrolytic Capacitor [capacitance=1µF package="100 mil [THT, electrolytic]"]
  Power_plug1 = Power plug
  U1 = Voltage Regulator - 5V [package="TO220 [THT]"]
  C2 = Electrolytic Capacitor [capacitance=1µF package="100 mil [THT, electrolytic]"]
  C3 = Electrolytic Capacitor [capacitance=1µF package="100 mil [THT, electrolytic]"]
  R1 = Rotary Potentiometer (Small) [maximum_resistance=100kΩ package=THT]
  R2 = Rotary Potentiometer (Small) [maximum_resistance=100kΩ package=THT]
  R3 = Rotary Potentiometer (Small) [maximum_resistance=100kΩ package=THT]
  R4 = Rotary Potentiometer (Small) [maximum_resistance=100kΩ package=THT]
  LED1 = LED - 5mm [color="Red (633nm)" package="5 mm [THT]"]
  LED2 = LED - 5mm [color="Red (633nm)" package="5 mm [THT]"]
  LED3 = LED - 5mm [color="Red (633nm)" package="5 mm [THT]"]
  LED4 = LED - 5mm [color="Red (633nm)" package="5 mm [THT]"]
  LED5 = LED - 5mm [color="Red (633nm)" package="5 mm [THT]"]
  LED6 = LED - 5mm [color="Red (633nm)" package="5 mm [THT]"]
  LED7 = LED - 5mm [color="Red (633nm)" package="5 mm [THT]"]
  LED8 = LED - 5mm [color="Red (633nm)" package="5 mm [THT]"]
  LED9 = LED - 5mm [color="Red (633nm)" package="5 mm [THT]"]
  LED10 = LED - 5mm [color="Red (633nm)" package="5 mm [THT]"]
  J1 = Piezo Speaker
  S2 = Pushbutton [package="[THT]"]
  R5 = Resistor [tolerance=±5% resistance=220 package=THT]
  R6 = Resistor [tolerance=±5% resistance=220 package=THT]
  R7 = Resistor [tolerance=±5% resistance=220 package=THT]
  R8 = Resistor [tolerance=±5% resistance=220 package=THT]
  R9 = Resistor [tolerance=±5% resistance=220 package=THT]
  R10 = Resistor [tolerance=±5% resistance=220 package=THT]
  R11 = Resistor [tolerance=±5% resistance=220 package=THT]
  R12 = Resistor [tolerance=±5% resistance=220 package=THT]
  R13 = Resistor [tolerance=±5% resistance=220 package=THT]
  R14 = Resistor [tolerance=±5% resistance=220 package=THT]
  R15 = Resistor [tolerance=±5% resistance=220 package=THT]
  S3 = Pushbutton [package="[THT]"]
  S4 = Toggle Switch [package=THT]

nets:
  N1: Part1.RESET, S3.Pin_3, S3.Pin_4
  GND: Part1.GND, C1.-, Power_plug1.GND, U1.GND, C2.-, C3.-, R1.leg1, R2.leg1, R3.leg1, R4.leg1, J1.pin1, S2.Pin_1, S2.Pin_2, R6.Pin_1, R7.Pin_1, R8.Pin_1, R9.Pin_1, R10.Pin_1, R11.Pin_1, R12.Pin_1, R13.Pin_1, R14.Pin_1, R15.Pin_1, S3.Pin_1, S3.Pin_2
  N2: Part1.D2, LED1.anode
  N3: Part1.D3, LED2.anode
  N4: Part1.D4, LED3.anode
  N5: Part1.D5, LED4.anode
  N6: Part1.D6, LED5.anode
  N7: Part1.D7, LED6.anode
  N8: Part1.D8, LED7.anode
  N9: Part1.D9, J1.pin2
  N10: Part1.D10, LED8.anode
  N11: Part1.D11/MOSI, LED9.anode
  N12: Part1.D12/MISO, LED10.anode
  N13: Part1.VIN, C1.+, R1.leg2, R2.leg2, R3.leg2, R4.leg2, R5.Pin_0, S4.COM
  N14: Part1.A3, R4.wiper
  N15: Part1.A2, R3.wiper
  N16: Part1.A1, R2.wiper
  N17: Part1.A0, R1.wiper
  N18: Part1.D13/SCK, S2.Pin_3, S2.Pin_4, R5.Pin_1
  N19: Power_plug1.VCC, U1.input_voltage, C3.+
  N20: U1.output_voltage, C2.+, S4.L1
  N21: LED1.cathode, R6.Pin_0
  N22: LED2.cathode, R7.Pin_0
  N23: LED3.cathode, R8.Pin_0
  N24: LED4.cathode, R9.Pin_0
  N25: LED5.cathode, R10.Pin_0
  N26: LED6.cathode, R11.Pin_0
  N27: LED7.cathode, R12.Pin_0
  N28: LED8.cathode, R13.Pin_0
  N29: LED9.cathode, R14.Pin_0
  N30: LED10.cathode, R15.Pin_0
