# Fritzing sketch id1418_nano_dl3416_0 (saved by Fritzing 0.9.3b)
breadboards: 1

parts:
  Part1 = Arduino Nano (Rev3.0)
  DL3416 = IC, DIP package, 22 pins [chip_label=DL3416]

nets:
  GND: Part1.GND, DL3416.pin3, DL3416.pin11, DL3416.pin12
  N1: Part1.D2, DL3416.pin16
  N2: Part1.D3, DL3416.pin17
  N3: Part1.D4, DL3416.pin18
  N4: Part1.D5, DL3416.pin19
  N5: Part1.D6, DL3416.pin20
  N6: Part1.D7, DL3416.pin21
  N7: Part1.D8, DL3416.pin22
  N8: Part1.D9, DL3416.pin7
  N9: Part1.D10, DL3416.pin8
  N10: Part1.D11/MOSI, DL3416.pin9
  N11: Part1.D12/MISO, DL3416.pin4
  5V: Part1.5V, DL3416.pin1, DL3416.pin2, DL3416.pin5, DL3416.pin6, DL3416.pin10, DL3416.pin14
