# Fritzing sketch id1419_Untitled_Sketch_2_0 (saved by Fritzing 0.9.2b)
breadboards: 1

parts:
  부품1 = Arduino Uno (Rev3)
  부품4 = Bluetooth Mate Silver
  LED1 = LED - 5mm [color="Red (633nm)" package="5 mm [THT]"]
  M1 = DC Motor
  MotorShield = Arduino Motor Shield
  M2 = DC Motor
  VCC1 = Battery block 9V
  J1 = Piezo Speaker

nets:
  N1: 부품1.D9_PWM, J1.pin2
  N2: 부품1.D10_PWM/SS, LED1.anode
  GND: 부품1.GND, 부품4.GND, LED1.cathode, J1.pin1
  N3: 부품1.D2, 부품4.RX_5V
  N4: 부품1.D3_PWM, 부품4.TX_5V
  N5: 부품1.D4, MotorShield.D2
  N6: 부품1.D5_PWM, MotorShield.D3
  N7: 부품1.D6_PWM, MotorShield.D4
  N8: 부품1.D7, MotorShield.D5
  5V: 부품1.5V, 부품4.VCC
  N9: M1.pin_1, MotorShield.OUT1
  N10: M1.pin_2, MotorShield.OUT2
  N11: MotorShield.GND, VCC1.+
  N12: MotorShield.OUT3, M2.pin_1
  N13: MotorShield.OUT4, M2.pin_2
  N14: MotorShield.VIN, VCC1.-
