# Fritzing sketch id141_5_Position_Switch___Controlling_4_LEDs_0 (saved by Fritzing 0.7.0b)
breadboards: 1

parts:
  U1 = Arduino Mega
  IC1 = IC, DIP package, 8 pins [chip_label=IC spacing=300mil]
  LED1 = LED - 5mm [color="Red (633nm)" package="5 mm [THT]"]
  LED2 = LED - 5mm [color="Red (633nm)" package="5 mm [THT]"]
  LED3 = LED - 5mm [color="Red (633nm)" package="5 mm [THT]"]
  LED4 = LED - 5mm [color="Red (633nm)" package="5 mm [THT]"]

nets:
  N1: U1.GND, IC1.pin8, LED1.cathode, LED2.cathode, LED3.cathode, LED4.cathode
  N2: U1.D11, LED3.anode
  N3: U1.D10, LED4.anode
  N4: U1.D9, LED1.anode
  N5: U1.D8, LED2.anode
  N6: U1.D6, IC1.pin6
  N7: U1.D5, IC1.pin7
  N8: U1.D4, IC1.pin2
  N9: U1.D3, IC1.pin3
  N10: U1.D2, IC1.pin4
  N11: U1.+5V, IC1.pin5

notes:
  The IC chip there is actually a 5-position switch - there wasn't a pre-made part in the Fritzing parts bins
