# Fritzing sketch id1420_arpschuino2R2_0 (saved by Fritzing 0.9.3b)
circuit board: 8.7023cm x 6.69925cm
breadboards: 1

parts:
  XTAL = Crystal [frequency="16 Mhz" package=THT]
  22pf = Ceramic Capacitor [capacitance=22pF package="100 mil [THT, multilayer]"]
  22pf_2 = Ceramic Capacitor [capacitance=22pF package="100 mil [THT, multilayer]"]
  Z_9_1v = Zener Diode [part_number=1N4732A breakdown_voltage=9.1V package="300 mil [THT]"]
  R47 = Resistor [tolerance=±5% resistance=47 package=THT]
  D1 = Rectifier Diode [part_number=1N4001 package="300 mil [THT]"]
  R470 = Resistor [tolerance=±20% resistance=470 package=THT]
  R120 = Resistor [tolerance=±5% resistance=120 package=THT]
  jumper = male pin header, 2 pins [form="♂ (male)"]
  R10K = Resistor [tolerance=±5% resistance=10k package=THT]
  100nf = Ceramic Capacitor [capacitance=100nF package="100 mil [THT, multilayer]"]
  reset = Pushbutton [package="[THT]"]
  220uf = Electrolytic Capacitor [capacitance=0.22mF package="200 mil [THT, electrolytic]"]
  220uf_2 = Electrolytic Capacitor [capacitance=0.22mF package="200 mil [THT, electrolytic]"]
  PWR = LED - 3mm [color="Red (633nm)" package="3 mm [THT]"]
  R330 = Resistor [tolerance=±5% resistance=330 package=THT]
  DMX = LED - 3mm [color="Red (633nm)" package="3 mm [THT]"]
  3/5V = screw terminal, 2 pins
  ATmega_328 = MICROCONTROLLER [package=dil28-3]
  J2 = screw terminal, 3 pins
  J3 = screw terminal, 3 pins
  J4 = shrouded pin header, 10 pins [form="♂ (shrouded male)"]
  AREF = female pin header, 2 pins [form="♀ (female)"]
  vcc = female pin header, 1 pin [form="♀ (female)"]
  gnd = female pin header, 1 pin [form="♀ (female)"]
  R471 = Resistor [tolerance=±5% resistance=360 package=THT]
  LM317 = Voltage Regulator - Variable [package="TO220 [THT]"]
  R472 = Resistor [tolerance=±5% resistance=680 package=THT]
  R473 = Resistor [tolerance=±5% resistance=220 package=THT]
  3V_5V = female pin header, 3 pins [form="♀ (female)"]
  I2C = female alternating pin header, 6 pins [form="♀ (female)"]
  serial = male alternating pin header, 6 pins [form="♂ (male)"]
  10uf = Electrolytic Capacitor [capacitance=1µF package="100 mil [THT, electrolytic]"]
  J1 = screw terminal, 2 pins
  XLR2 = prefix0000
  XLR3 = prefix0000
  rs485 = rs 485 [chip_label=RS485]
  J5 = shrouded pin header, 10 pins [form="♂ (shrouded male)"]
  J6 = female pin header, 1 pin [form="♀ (female)"]
  J7 = female pin header, 1 pin [form="♀ (female)"]

nets:
  N1: XTAL.pin_0, 22pf_2.1, ATmega_328.PB7(XTAL2_TOSC2)
  N2: XTAL.pin_1, 22pf.1, ATmega_328.PB6(XTAL1_TOSC1)
  GND: 22pf.0, 22pf_2.0, Z_9_1v.anode, 100nf.0, reset.Pin_1, reset.Pin_2, 220uf.-, 220uf_2.-, PWR.cathode, 3/5V.pin1, ATmega_328.GND, ATmega_328.AGND, J2.pin1, J3.pin1, J4.pin7, gnd.pin1, R471.Pin_0, R472.Pin_0, I2C.pin1, serial.pin1, 10uf.-, J1.pin1, XLR2.connector0, XLR2.connector5, XLR2.connector6, XLR3.connector7, XLR3.connector12, XLR3.connector14, rs485.connector4, J5.pin7, J6.pin1
  9V: Z_9_1v.cathode, R47.Pin_1, 220uf.+, LM317.IN
  N3: R47.Pin_0, D1.cathode, 220uf_2.+
  12V: D1.anode, J1.pin2
  N4: R470.Pin_0, PWR.anode
  5V: R470.Pin_1, R10K.Pin_1, 100nf.1, R330.Pin_1, 3/5V.pin2, ATmega_328.VCC, ATmega_328.AVCC, J4.pin8, vcc.pin1, LM317.OUT, R473.Pin_1, I2C.pin5, serial.pin3, 10uf.+, rs485.connector7, J5.pin8, J7.pin1
  N5: R120.Pin_0, J2.pin3, J3.pin3, XLR2.connector1, XLR2.connector7, XLR3.connector8, XLR3.connector13, rs485.connector6
  N6: R120.Pin_1, J2.pin2, J3.pin2, XLR2.connector2, XLR3.connector9, rs485.connector5
  rx: jumper.pin1, ATmega_328.PD0(RXD), serial.pin4
  N7: jumper.pin2, rs485.connector0
  N8: R10K.Pin_0, reset.Pin_3, reset.Pin_4, ATmega_328.PC6(_RESET), serial.pin6
  N9: R330.Pin_0, DMX.anode
  N10: DMX.cathode, ATmega_328.PD4(XCK_T0)
  tx: ATmega_328.PD1(TXD), serial.pin5, rs485.connector3
  N11: ATmega_328.PD2(INT0), J5.pin6
  N12: ATmega_328.PD3(INT1), J4.pin6
  N13: ATmega_328.PD5(T1), J4.pin5
  N14: ATmega_328.PD6(AIN0), J4.pin4
  N15: ATmega_328.PD7(AIN1), rs485.connector1, rs485.connector2
  N16: ATmega_328.PB0(ICP), J5.pin5
  N17: ATmega_328.PB1(OC1A), J4.pin1
  N18: ATmega_328.PB2(SS_OC1B), J4.pin10
  N19: ATmega_328.PB3(MOSI_OC2), J4.pin9
  N20: ATmega_328.PB4(MISO), J4.pin2
  N21: ATmega_328.PB5(SCK), J4.pin3
  N22: ATmega_328.AREF, AREF.pin1, AREF.pin2
  N23: ATmega_328.PC0(ADC0), J5.pin4
  N24: ATmega_328.PC1(ADC1), J5.pin3
  N25: ATmega_328.PC2(ADC2), J5.pin2
  N26: ATmega_328.PC3(ADC3), J5.pin1
  A4: ATmega_328.PC4(ADC4_SDA), I2C.pin4, J5.pin10
  A5: ATmega_328.PC5(ADC5_SCL), I2C.pin3, J5.pin9
  N27: R471.Pin_1, 3V_5V.pin1
  N28: LM317.ADJ, R473.Pin_0, 3V_5V.pin2
  N29: R472.Pin_1, 3V_5V.pin3

notes:
  6>15V
  +  -
  in
  DMX
  vcc
  gnd
  D3~
  D11~
  D9~
  D8
  D2
  D6~
  D5~
  D10~
  D12
  A5
  A4
  A3
  A1
  A2
  A0
  D13
  +
  -
  Corrections :
  + - Vin
  10K ohm
  680 ohm au lieu de 665
  diode de protection en tete
  leds déplacees
  atmega, 485 et reset déplacés vers la gauche
  trous de fixations M3
  diode de protection en tête
  empreinte pour mini potar aref
  XLR !
  sda
  scl
  V+
  rx
  tx
  rst
  designed by J Boüault
  arpschuino²
  FAIT:
  -supression du jumper dmx out.
  -changement de l'empreinte de l'atmega
  pistes plus fines.
  -troux bornier dmx plus fin.
  -atmega et max un cran plus bas.
  -R470 ohms pour la led rouge(vérifier)
  -retournement des borniers alim et dmx retournés
  power dans la nappe
  Aref modifiable par pont
  3.3v possible
  leds deplacees
  trous des ports serial et I2C alternatifs
  DMX in
  D-D+Gnd
  arpschuino.fr
  alim :
  mode 3.3V :
  5V>15V
  mode 5V :
  7V> 15V
  R1=220, R2=680, Vout=5.148V
  R1=231, R2=673, Vout=4.925V
  R1=209, R2=687, Vout=5.393V
  R1=220, R2=360, Vout=3.313V
  R1=231, R2=356, Vout=3.194V
  R1=209, R2=364, Vout=3.445V
  out
  R2
  R2 : XLR version
  a
