# Fritzing sketch id1421_DMXLight_0 (saved by Fritzing 0.9.2b)
circuit board: 6.88566cm x 5.36311cm
breadboards: 1

parts:
  MAX485 = IC, DIP package, 8 pins [chip_label=MAX485]
  100 = Resistor [tolerance=±5% resistance=100 package=THT]
  23LC1024 = IC, DIP package, 8 pins [chip_label=23LC1024]
  10K = Resistor [tolerance=±5% resistance=10k package=THT]
  DIP1 = DIP SWITCH [package=dipswitch-02]
  DIP2 = DIP SWITCH [package=dipswitch-02]
  J1 = female pin header, 3 pins [form="♀ (female)"]
  A/B_Change = female pin header, 3 pins [form="♀ (female)"]
  Off/Prog/On = female pin header, 3 pins [form="♀ (female)"]
  DMX = female pin header, 3 pins [form="♀ (female)"]
  10K_2 = Resistor [tolerance=±5% resistance=10k package=THT]
  10K_3 = Resistor [tolerance=±5% resistance=10k package=THT]
  J2 = female pin header, 3 pins [form="♀ (female)"]
  DMXLight_V1_2_-_(C)_H_Wirtz = prefix0000

nets (from the breadboard view):
  N1: MAX485.pin1, 100.Pin_1
  N2: MAX485.pin2, MAX485.pin5, 100.Pin_0, 23LC1024.pin4, DIP1.1, DIP1.2, DIP2.1, DIP2.2, Off/Prog/On.pin2, DMX.pin2, J2.pin3, DMXLight_V1_2_-_(C)_H_Wirtz.connector88
  N3: MAX485.pin3, MAX485.pin8, 23LC1024.pin8, 10K.Pin_0, 10K_2.Pin_1, 10K_3.Pin_0, J2.pin1, DMXLight_V1_2_-_(C)_H_Wirtz.connector87
  N4: MAX485.pin4, DMXLight_V1_2_-_(C)_H_Wirtz.connector63
  N5: MAX485.pin6, A/B_Change.pin2
  N6: MAX485.pin7, J1.pin2
  N7: 23LC1024.pin1, 10K.Pin_1, DMXLight_V1_2_-_(C)_H_Wirtz.connector53
  N8: 23LC1024.pin2, DMXLight_V1_2_-_(C)_H_Wirtz.connector39
  N9: 23LC1024.pin3, 10K_3.Pin_1
  N10: 23LC1024.pin5, DMXLight_V1_2_-_(C)_H_Wirtz.connector42
  N11: 23LC1024.pin6, DMXLight_V1_2_-_(C)_H_Wirtz.connector41
  N12: 23LC1024.pin7, 10K_2.Pin_0
  N13: DIP1.3, DMXLight_V1_2_-_(C)_H_Wirtz.connector65
  N14: DIP1.4, DMXLight_V1_2_-_(C)_H_Wirtz.connector66
  N15: DIP2.3, DMXLight_V1_2_-_(C)_H_Wirtz.connector67
  N16: DIP2.4, DMXLight_V1_2_-_(C)_H_Wirtz.connector68
  N17: J1.pin1, A/B_Change.pin3, DMX.pin1
  N18: J1.pin3, A/B_Change.pin1, DMX.pin3
  N19: Off/Prog/On.pin1, DMXLight_V1_2_-_(C)_H_Wirtz.connector51
  N20: Off/Prog/On.pin3, DMXLight_V1_2_-_(C)_H_Wirtz.connector52
  N21: J2.pin2, DMXLight_V1_2_-_(C)_H_Wirtz.connector0

notes:
  DMX signal inverted
  DMX signal
  DMX
  Switch 2*3
  Switch 1*3
  DMXLight shield V1.2
  (C) H. Wirtz
  1 2 3 4 5 6
