# Fritzing sketch id1422_Dome_Exterior_0 (saved by Fritzing 0.9.2b)
breadboards: 2

parts:
  Part1 = Spark Core (v1.0)
  U3 = mystery part, 3 pins [chip_label=?]
  U4 = mystery part, 3 pins [chip_label=?]
  RHT1 = Humidity and Temperature Sensor RHT03
  U5 = mystery part, 3 pins [chip_label=?]
  U6 = mystery part, 3 pins [chip_label=?]
  U7 = mystery part, 3 pins [chip_label=?]
  U8 = mystery part, 3 pins [chip_label=?]
  U9 = mystery part, 3 pins [chip_label=?]
  R2 = Resistor [tolerance=±5% resistance=10k package="2512 [SMD]"]
  R3 = Resistor [tolerance=±5% resistance=4.7k package=THT]
  R4 = Resistor [tolerance=±5% resistance=4.7k package=THT]

nets:
  N1: Part1.D0, U5.pin2
  N2: Part1.D1, U6.pin2
  N3: Part1.D2, U7.pin2
  N4: Part1.D3, U8.pin2
  N5: Part1.D4, U9.pin2
  N6: Part1.D5, RHT1.Data-signal, R2.Pin_1
  N7: Part1.D6, U4.pin2, R3.Pin_0
  N8: Part1.D7, U3.pin2, R4.Pin_0
  N9: Part1.3V3*, U3.pin3, U4.pin3, RHT1.Vcc, U5.pin3, U6.pin3, U7.pin3, U8.pin3, U9.pin3, R2.Pin_0, R3.Pin_1, R4.Pin_1
  N10: U3.pin1, U4.pin1, RHT1.GND_1, U5.pin1, U6.pin1, U7.pin1, U8.pin1, U9.pin1

notes:
  These mystery parts are RTD's.
  These mystery parts are flowmeters.
