# Fritzing sketch id1423_Dome_Interior_0 (saved by Fritzing 0.9.2b)
breadboards: 2

parts:
  Part1 = Spark Core (v1.0)
  RHT1 = Humidity and Temperature Sensor RHT03
  R1 = Temperature Sensor (Thermistor) [thermistor_type=NTC package=THT]
  R2 = Temperature Sensor (Thermistor) [thermistor_type=NTC package=THT]
  R4 = Resistor [tolerance=±5% resistance=10k package=THT]
  R3 = Resistor [tolerance=±5% resistance=10k package=THT]

nets:
  N1: Part1.A0, R1.pin_1, R4.Pin_0
  N2: Part1.A1, R2.pin_1, R3.Pin_0
  N3: Part1.GND, RHT1.GND_1, R4.Pin_1, R3.Pin_1
  N4: Part1.D2, RHT1.Data-signal
  N5: Part1.3V3*, RHT1.Vcc, R1.pin_0, R2.pin_0
