# Fritzing sketch id1424_Dome_Side_0 (saved by Fritzing 0.9.2b)
breadboards: 2

parts:
  Part2 = Spark Core (v1.0)
  U10 = mystery part, 3 pins [chip_label=?]
  U11 = mystery part, 3 pins [chip_label=?]
  R6 = Resistor [tolerance=±5% resistance=4.7k package=THT]
  R7 = Resistor [tolerance=±5% resistance=4.7k package=THT]

nets:
  N1: Part2.D6, U11.pin2, R7.Pin_0
  N2: Part2.D7, U10.pin2, R6.Pin_0
  N3: Part2.3V3*, U10.pin3, U11.pin3, R6.Pin_1, R7.Pin_1
  N4: U10.pin1, U11.pin1

notes:
  These mystery parts are RTD's.
