# Fritzing sketch id1425_House_0 (saved by Fritzing 0.9.2b)
circuit board: 10.4098cm x 12.646cm
breadboards: 1

parts:
  LED1 = RGB LED - (4 legs) [package="5 mm [THT]"]
  LED2 = RGB LED - (4 legs) [package="5 mm [THT]"]
  LED4 = RGB LED - (4 legs) [package="5 mm [THT]"]
  Q1 = NPN-Transistor [package="TO92 [THT]"]
  Q2 = NPN-Transistor [package="TO92 [THT]"]
  Q3 = NPN-Transistor [package="TO92 [THT]"]
  Q4 = NPN-Transistor [package="TO92 [THT]"]
  Q5 = NPN-Transistor [package="TO92 [THT]"]
  Q6 = NPN-Transistor [package="TO92 [THT]"]
  Q7 = NPN-Transistor [package="TO92 [THT]"]
  Q8 = NPN-Transistor [package="TO92 [THT]"]
  Q9 = NPN-Transistor [package="TO92 [THT]"]
  Q10 = NPN-Transistor [package="TO92 [THT]"]
  Q11 = NPN-Transistor [package="TO92 [THT]"]
  Q12 = NPN-Transistor [package="TO92 [THT]"]
  R1 = Resistor [tolerance=±5% resistance=14.7k package=THT]
  R2 = Resistor [tolerance=±5% resistance=14.7k package=THT]
  R3 = Resistor [tolerance=±5% resistance=14.7k package=THT]
  R4 = Resistor [tolerance=±5% resistance=14.7k package=THT]
  R5 = Resistor [tolerance=±5% resistance=30k package=THT]
  R6 = Resistor [tolerance=±5% resistance=14.7k package=THT]
  R7 = Resistor [tolerance=±5% resistance=14.7k package=THT]
  R8 = Resistor [tolerance=±5% resistance=14.7k package=THT]
  R9 = Resistor [tolerance=±5% resistance=14.7k package=THT]
  R10 = Resistor [tolerance=±5% resistance=14.7k package=THT]
  R11 = Resistor [tolerance=±5% resistance=14.7k package=THT]
  R12 = Resistor [tolerance=±5% resistance=14.7k package=THT]
  R13 = Resistor [tolerance=±5% resistance=200 package=THT]
  R14 = Resistor [tolerance=±5% resistance=200 package=THT]
  R15 = Resistor [tolerance=±5% resistance=200 package=THT]
  R16 = Resistor [tolerance=±5% resistance=200 package=THT]
  R17 = Resistor [tolerance=±5% resistance=100 package=THT]
  R18 = Resistor [tolerance=±5% resistance=100 package=THT]
  R20 = Resistor [tolerance=±5% resistance=100 package=THT]
  R21 = Resistor [tolerance=±5% resistance=100 package=THT]
  R22 = Resistor [tolerance=±5% resistance=100 package=THT]
  R23 = Resistor [tolerance=±5% resistance=100 package=THT]
  R24 = Resistor [tolerance=±5% resistance=100 package=THT]
  R19 = Resistor [tolerance=±5% resistance=100 package=THT]
  LED5 = LED - 5mm [color="White (4500K)" package="5 mm [THT]"]
  LED6 = LED - 5mm [color="White (4500K)" package="5 mm [THT]"]
  LED7 = LED - 5mm [color="White (4500K)" package="5 mm [THT]"]
  LED8 = LED - 5mm [color="White (4500K)" package="5 mm [THT]"]
  LED9 = LED - 5mm [color="White (4500K)" package="5 mm [THT]"]
  LED10 = LED - 5mm [color="White (4500K)" package="5 mm [THT]"]
  LED3 = RGB LED - (4 legs) [package="5 mm [THT]"]
  Parte1 = Arduino Mega 2560 (Rev3)
  S1 = SWITCH-MOMENTARY-2 [package=tactile_switch_smd-2]
  S2 = SWITCH-MOMENTARY-2 [package=tactile_switch_smd-2]
  S3 = SWITCH-MOMENTARY-2 [package=tactile_switch_smd-2]
  S4 = SWITCH-MOMENTARY-2 [package=tactile_switch_smd-2]
  S5 = SWITCH-MOMENTARY-2 [package=tactile_switch_smd-2]
  S6 = SWITCH-MOMENTARY-2 [package=tactile_switch_smd-2]

nets:
  N1: LED1.red_cathode, Q1.C
  N2: LED1.common_anode, LED2.common_anode, LED4.common_anode, LED3.common_anode, Parte1.5V
  N3: LED1.green_cathode, Q2.C
  N4: LED1.blue_cathode, Q3.C
  N5: LED2.red_cathode, Q4.C
  N6: LED2.green_cathode, Q5.C
  N7: LED2.blue_cathode, Q6.C
  N8: LED4.red_cathode, Q10.C
  N9: LED4.green_cathode, Q11.C
  N10: LED4.blue_cathode, Q12.C
  N11: Q1.E, R13.Pin_0
  N12: Q1.B, R1.Pin_1
  N13: Q2.E, R17.Pin_0
  N14: Q2.B, R5.Pin_1
  N15: Q3.E, R18.Pin_0
  N16: Q3.B, R6.Pin_1
  N17: Q4.E, R14.Pin_0
  N18: Q4.B, R4.Pin_1
  N19: Q5.E, R19.Pin_0
  N20: Q5.B, R7.Pin_1
  N21: Q6.E, R20.Pin_0
  N22: Q6.B, R8.Pin_1
  N23: Q7.E, R15.Pin_1
  N24: Q7.B, R12.Pin_0
  N25: Q7.C, LED3.red_cathode
  N26: Q8.E, R21.Pin_1
  N27: Q8.B, R11.Pin_0
  N28: Q8.C, LED3.green_cathode
  N29: Q9.E, R22.Pin_1
  N30: Q9.B, R2.Pin_0
  N31: Q9.C, LED3.blue_cathode
  N32: Q10.E, R16.Pin_1
  N33: Q10.B, R10.Pin_0
  N34: Q11.E, R23.Pin_1
  N35: Q11.B, R9.Pin_0
  N36: Q12.E, R24.Pin_1
  N37: Q12.B, R3.Pin_0
  N38: R1.Pin_0, Parte1.D2_PWM
  N39: R2.Pin_1, Parte1.D10_PWM
  N40: R3.Pin_1, Parte1.D13_PWM
  N41: R4.Pin_0, Parte1.D5_PWM
  N42: R5.Pin_0, Parte1.D3_PWM
  N43: R6.Pin_0, Parte1.D4_PWM
  N44: R7.Pin_0, Parte1.D6_PWM
  N45: R8.Pin_0, Parte1.D7_PWM
  N46: R9.Pin_1, Parte1.D12_PWM
  N47: R10.Pin_1, Parte1.D11_PWM
  N48: R11.Pin_1, Parte1.D9_PWM
  N49: R12.Pin_1, Parte1.D8_PWM
  N50: R13.Pin_1, R14.Pin_1, R15.Pin_0, R16.Pin_0, R17.Pin_1, R18.Pin_1, R20.Pin_1, R21.Pin_0, R22.Pin_0, R23.Pin_0, R24.Pin_0, R19.Pin_1, LED5.cathode, LED6.cathode, LED7.cathode, LED8.cathode, LED9.cathode, LED10.cathode, Parte1.GND
  N51: LED5.anode, Parte1.A1
  N52: LED6.anode, Parte1.A2
  N53: LED7.anode, Parte1.A3
  N54: LED8.anode, Parte1.A4
  N55: LED9.anode, Parte1.A5
  N56: LED10.anode, Parte1.A6
  N57: Parte1.D24, S6.1
  N58: Parte1.D26, S6.2
  N59: Parte1.D28, S5.1
  N60: Parte1.D30, S5.2
  N61: Parte1.D32, S4.1
  N62: Parte1.D34, S4.2
  N63: Parte1.D36, S3.1
  N64: Parte1.D38, S3.2
  N65: Parte1.D40, S2.1
  N66: Parte1.D42, S2.2
  N67: Parte1.D44, S1.1
  N68: Parte1.D46, S1.2
