# Fritzing sketch id1427_Untitled_Sketch_2_0 (saved by Fritzing 0.9.3b)
breadboards: 1

parts:
  Raspberry_Pi_1 = Raspberry Pi 3 [part_number=RPI-3-V1.2]
  U1 = TRANSISTOR_NPN_2 [package=to-92]
  U2 = TRANSISTOR_NPN_2 [package=to-92]
  S1 = SWITCH-MOMENTARY-2 [package=reed_switch_plastic]
  S4 = Round Pushbutton
  R1 = Resistor [tolerance=±5% resistance=220 package=THT]
  U8 = RELAY [package=OJ]
  U13 = RELAY [package=OJ]
  J1 = Basic Servo
  VCC1 = Battery block 9V

nets:
  N1: Raspberry_Pi_1.GPIO6, U1.B
  N2: Raspberry_Pi_1.GPIO16, S1.1
  GND: Raspberry_Pi_1.GND, U1.E, U2.E, R1.Pin_1, J1.gnd, VCC1.-
  N3: Raspberry_Pi_1.GPIO12, U2.B
  N4: Raspberry_Pi_1.5V, U8.COIL2, U13.COIL2
  N5: U1.C, U8.COIL1
  N6: U2.C, U13.COIL1
  N7: S4.leg0, U8.MAIN
  N8: S4.leg1, U8.NO
  N9: U13.MAIN, VCC1.+
  N10: U13.NO, J1.vcc

notes:
  Intercom Door Switch
  Door Key Servo
  Door Magnetic Switch
  Power Supply
