# Fritzing sketch id142_5_Position_Switch___Controlling_4_LEDs_1_0 (saved by Fritzing 0.8.7b)
breadboards: 1

parts:
  IC1 = IC, DIP package, 8 pins [chip_label=IC spacing=300mil]
  LED1 = LED - 5mm [color="Red (633nm)" package="5 mm [THT]"]  # not connected
  LED2 = LED - 5mm [color="Red (633nm)" package="5 mm [THT]"]  # not connected
  LED3 = LED - 5mm [color="Red (633nm)" package="5 mm [THT]"]
  LED4 = LED - 5mm [color="Red (633nm)" package="5 mm [THT]"]  # not connected
  R1 = Resistor [tolerance=±5% resistance=470 package=THT]
  R2 = Resistor [tolerance=±5% resistance=470 package=THT]  # not connected
  R3 = Resistor [tolerance=±5% resistance=470 package=THT]  # not connected
  U1 = Arduino Uno (Rev3)
  R4 = Resistor [tolerance=±5% resistance=470 package=THT]

nets:
  N1: IC1.pin8, R1.Pin_0
  N2: LED3.cathode, R4.Pin_0
  N3: U1.GND, R4.Pin_1

notes:
  The IC chip there is actually a 5-position switch - there wasn't a pre-made part in the Fritzing parts bins
