# Fritzing sketch id1430_WifiDoorSensor3_0 (saved by Fritzing 0.9.0b)
breadboards: 1

parts:
  C1 = Electrolytic Capacitor [capacitance=10µF package="100 mil [THT, electrolytic]"]
  C2 = Electrolytic Capacitor [capacitance=10µF package="100 mil [THT, electrolytic]"]
  S1 = Toggle Switch [package=THT]
  R1 = Resistor [tolerance=±5% resistance=220 package=THT]
  U2 = ESP8266_module [part_number=ESP8266]
  Q1 = NPN-Transistor [part_number=BC337 package="TO92 [THT]"]
  U4 = LM1117T [part_number=LM1117T]
  VCC1 = Battery block 9V
  R3 = Resistor [tolerance=±5% resistance=6k package=THT]

nets (from the schematic view):
  N1: C1.-, C2.-, U2.connector6, U4.connector1, VCC1.-
  N2: C1.+, S1.COM, Q1.C, U4.connector2
  N3: C2.+, U4.connector0, VCC1.+
  N4: S1.L1, R3.Pin_1
  N5: S1.L2, U2.connector1, Q1.E
  N6: R1.Pin_0, U2.connector2
  N7: U2.connector4, R3.Pin_0

notes:
  door open
  door closed
