# Fritzing sketch id1432_atozpc_adruino_yun_doorbeel_1_0 (saved by Fritzing 0.9.0b)
breadboards: 1

parts:
  U2 = Transformer [package=transformer]
  S2 = Pushbutton [package=THT]
  SG1 = Buzzer 12mm [package=buzzer-ccv-kit]  # not connected
  R2 = Resistor [tolerance=±5% resistance=1k package=THT]
  D2 = Rectifier Diode [part_number=1N4001 package="300 mil [THT]"]
  Part2 = Arduino Yun
  Q1 = Basic FET P-Channel [package="TO220 [THT]"]
  R3 = Resistor [tolerance=±5% resistance=220 package=THT]

nets:
  N1: U2.2, R2.Pin_0
  N2: S2.leg0, D2.cathode, Part2.D3_PWM, Q1.drain, R3.Pin_0
  N3: R2.Pin_1, Part2.5V, Q1.gate
  N4: Part2.GND, R3.Pin_1

notes:
  Doorbell
  110V to 16V Transformer
  Doorbell button
  WALL
