# Fritzing sketch id1433_DOORBELL_0 (saved by Fritzing 0.3.19b)
breadboards: 1

parts:
  S1 = Pushbutton [package=THT]
  LED1 = white LED - 5mm
  L1 = Solenoid
  R1 = Resistor [resistance=10k package=THT]
  Power_plug1 = Power plug

nets:
  N1: S1.leg0, L1.pin2, R1.Pin_0
  N2: S1.leg1, LED1.cathode, Power_plug1.GND
  N3: LED1.anode, R1.Pin_1
  N4: L1.pin1, Power_plug1.VCC

notes:
  This is the basic principle behind a doorbell.
  The 10k resistor is to protect the circuit.
  Solenoid strikes bell.
