# Fritzing sketch id1434_DoorPi_Teststellung_0 (saved by Fritzing 0.9.2b)
breadboards: 1

parts:
  Raspberry_Pi1 = Raspberry_Pi__Model_B
  LED1 = LED - 3mm [color="Red (633nm)" package="3 mm [THT]"]
  R1 = Resistor [tolerance=±20% resistance=1k package=THT]
  LED2 = LED - 3mm [color="Green (565nm)" package="3 mm [THT]"]
  LED3 = LED - 3mm [color="Yellow (592nm)" package="3 mm [THT]"]
  R2 = Resistor [tolerance=±20% resistance=1k package=THT]
  R3 = Resistor [tolerance=±20% resistance=1k package=THT]
  R4 = Resistor [tolerance=±20% resistance=1k package=THT]
  R5 = Resistor [tolerance=±20% resistance=10k package=THT]
  S1 = Pushbutton [package="[SMD]"]
  R6 = Resistor [tolerance=±20% resistance=10k package=THT]
  R7 = Resistor [tolerance=±20% resistance=10k package=THT]
  S2 = Pushbutton [package="[SMD]"]
  S3 = Pushbutton [package="[SMD]"]

nets:
  N1: Raspberry_Pi1.connector6, LED1.anode, LED2.anode, LED3.anode, R5.Pin_1, R6.Pin_1, R7.Pin_1
  N2: Raspberry_Pi1.connector7, R2.Pin_0
  N3: Raspberry_Pi1.connector11, R6.Pin_0, S3.Pin_3, S3.Pin_4
  N4: Raspberry_Pi1.connector13, R7.Pin_0, S2.Pin_3, S2.Pin_4
  N5: Raspberry_Pi1.connector15, R5.Pin_0, S1.Pin_3, S1.Pin_4
  N6: Raspberry_Pi1.connector16, R1.Pin_0
  N7: Raspberry_Pi1.connector18, R3.Pin_0
  N8: LED1.cathode, R1.Pin_1
  N9: LED2.cathode, R2.Pin_1
  N10: LED3.cathode, R3.Pin_1
  N11: R4.Pin_1, S1.Pin_1, S1.Pin_2, S2.Pin_1, S2.Pin_2, S3.Pin_1, S3.Pin_2
