# Fritzing sketch id1435_dos_motorescon_joystick_0 (saved by Fritzing 0.9.1b)
breadboards: 1

parts:
  Parte1 = Arduino Uno (Rev3)
  M1 = DC Motor
  M2 = DC Motor
  IC1 = L293D [package=THT]
  VCC1 = Battery block 9V  # not connected
  Parte2 = Thumb Joystick

nets:
  N1: Parte1.A0, Parte2.VERT
  N2: Parte1.A1, Parte2.HORZ
  N3: Parte1.D9_PWM, IC1.In_1
  N4: Parte1.D10_PWM/SS, IC1.In_2
  N5: Parte1.D5_PWM, IC1.In_3
  N6: Parte1.D6_PWM, IC1.In_4
  5V: Parte1.5V, IC1.+V, Parte2.VCC
  GND: Parte1.GND, IC1.0V, Parte2.GND
  N7: M1.pin_1, IC1.Out_3_(_Controlled_by_Enable_2_)
  N8: M1.pin_2, IC1.Out_4_(_Controlled_by_Enable_2_)
  N9: M2.pin_1, IC1.Out_2_(_Controlled_by_Enable_1_)
  N10: M2.pin_2, IC1.Out_1_(_Controlled_by_Enable_1_)
