# Fritzing sketch id1436_74HC595_0 (saved by Fritzing 0.9.3b)
circuit board: 7.77659cm x 3.42567cm
breadboards: 1

parts:
  U1 = 74HC595 [package="DIP16 [THT]"]
  SEGMENT_1 = female pin header, 8 pins [form="♀ (female)"]
  U2 = 74HC595 [package="DIP16 [THT]"]
  SEGMENT_2 = female pin header, 8 pins [form="♀ (female)"]
  INPUT = female pin header, 5 pins [form="♀ (female)"]
  OUTPUT = female pin header, 5 pins [form="♀ (female)"]

nets:
  N1: U1.Q1, SEGMENT_1.pin2
  N2: U1.Q2, SEGMENT_1.pin3
  N3: U1.Q3, SEGMENT_1.pin4
  N4: U1.Q4, SEGMENT_1.pin5
  N5: U1.Q5, SEGMENT_1.pin6
  N6: U1.Q6, SEGMENT_1.pin7
  N7: U1.Q7, SEGMENT_1.pin8
  GND: U1.GND, U1.OE, U2.GND, U2.OE, INPUT.pin1, OUTPUT.pin1
  N8: U1.Q7', U2.DS
  VCC: U1.MR, U1.VCC, U2.MR, U2.VCC, INPUT.pin3, OUTPUT.pin3
  N9: U1.SH_CP, U2.SH_CP, INPUT.pin5, OUTPUT.pin5
  N10: U1.ST_CP, U2.ST_CP, INPUT.pin4, OUTPUT.pin4
  N11: U1.DS, INPUT.pin2
  N12: U1.Q0, SEGMENT_1.pin1
  N13: U2.Q1, SEGMENT_2.pin2
  N14: U2.Q2, SEGMENT_2.pin3
  N15: U2.Q3, SEGMENT_2.pin4
  N16: U2.Q4, SEGMENT_2.pin5
  N17: U2.Q5, SEGMENT_2.pin6
  N18: U2.Q6, SEGMENT_2.pin7
  N19: U2.Q7, SEGMENT_2.pin8
  N20: U2.Q7', OUTPUT.pin2
  N21: U2.Q0, SEGMENT_2.pin1
