# Fritzing sketch id1437_74HC595_uln2803_rotate_0 (saved by Fritzing 0.9.3b)
circuit board: 8.03071cm x 4.30153cm
breadboards: 1

parts:
  U1 = 74HC595 [package="DIP16 [THT]"]
  U2 = 74HC595 [package="DIP16 [THT]"]
  1112+D- = female pin header, 5 pins [form="♀ (female)"]
  1112+D-_2 = female pin header, 5 pins [form="♀ (female)"]
  SEGMENT_5 = female pin header, 8 pins [form="♀ (female)"]
  IC1 = ULN2803A [package=THT]
  SEGMENT_6 = female pin header, 8 pins [form="♀ (female)"]
  IC2 = ULN2803A [package=THT]
  -+ = female pin header, 2 pins [form="♀ (female)"]
  -_+ = female pin header, 2 pins [form="♀ (female)"]

nets:
  N1: U1.Q1, IC1.In_7
  N2: U1.Q2, IC1.In_6
  N3: U1.Q3, IC1.In_5
  N4: U1.Q4, IC1.In_4
  N5: U1.Q5, IC1.In_3
  N6: U1.Q6, IC1.In_2
  N7: U1.Q7, IC1.In_1
  GND: U1.GND, U1.OE, U2.GND, U2.OE, 1112+D-.pin1, 1112+D-_2.pin1, IC1.0V, IC2.0V, -+.pin2, -_+.pin2
  N8: U1.Q7', U2.DS
  VCC: U1.MR, U1.VCC, U2.MR, U2.VCC, 1112+D-.pin3, 1112+D-_2.pin3
  N9: U1.SH_CP, U2.SH_CP, 1112+D-.pin5, 1112+D-_2.pin5
  N10: U1.ST_CP, U2.ST_CP, 1112+D-.pin4, 1112+D-_2.pin4
  N11: U1.DS, 1112+D-.pin2
  N12: U1.Q0, IC1.In_8
  N13: U2.Q1, IC2.In_7
  N14: U2.Q2, IC2.In_6
  N15: U2.Q3, IC2.In_5
  N16: U2.Q4, IC2.In_4
  N17: U2.Q5, IC2.In_3
  N18: U2.Q6, IC2.In_2
  N19: U2.Q7, IC2.In_1
  N20: U2.Q7', 1112+D-_2.pin2
  N21: U2.Q0, IC2.In_8
  N22: SEGMENT_5.pin1, IC1.Out_1
  N23: SEGMENT_5.pin2, IC1.Out_2
  N24: SEGMENT_5.pin3, IC1.Out_3
  N25: SEGMENT_5.pin4, IC1.Out_4
  N26: SEGMENT_5.pin5, IC1.Out_5
  N27: SEGMENT_5.pin6, IC1.Out_6
  N28: SEGMENT_5.pin7, IC1.Out_7
  N29: SEGMENT_5.pin8, IC1.Out_8
  N30: IC1.COM_-_Common, IC2.COM_-_Common, -+.pin1, -_+.pin1
  N31: SEGMENT_6.pin1, IC2.Out_1
  N32: SEGMENT_6.pin2, IC2.Out_2
  N33: SEGMENT_6.pin3, IC2.Out_3
  N34: SEGMENT_6.pin4, IC2.Out_4
  N35: SEGMENT_6.pin5, IC2.Out_5
  N36: SEGMENT_6.pin6, IC2.Out_6
  N37: SEGMENT_6.pin7, IC2.Out_7
  N38: SEGMENT_6.pin8, IC2.Out_8
