# Fritzing sketch id1438_LED_RJ45_Breakout_0 (saved by Fritzing 0.8.3b)
circuit board: 9cm x 3.5cm
breadboards: 1

parts:
  U1 = RJ45 Jack [package=rj45-8]
  J1 = female pin header, 3 pins [form="♀ (female)"]
  J2 = female pin header, 3 pins [form="♀ (female)"]

nets:
  N1: U1.1, J2.pin1
  N2: U1.2, J1.pin1
  N3: U1.3, J2.pin2
  N4: U1.4, J1.pin2
  N5: U1.5, J2.pin3
  N6: U1.6, J1.pin3
