# Fritzing sketch id1439_RGB_So_Groovy_ATM328_ethernet_0 (saved by Fritzing 0.8.7b)
circuit board: 16cm x 10cm
breadboards: 1

parts:
  V1T = Basic FET N-Channel [package="TO220 [THT]"]
  R1T = Basic FET N-Channel [package="TO220 [THT]"]
  V2T = Basic FET N-Channel [package="TO220 [THT]"]
  ResB2R = Resistor [tolerance=±5% resistance=3.6 power=2 package=THT]
  ResR1R = Resistor [tolerance=±5% resistance=3.6 power=2 package=THT]
  ResV2R = Resistor [tolerance=±5% resistance=3.6 power=2 package=THT]
  B2T = Basic FET N-Channel [package="TO220 [THT]"]
  B1T = Basic FET N-Channel [package="TO220 [THT]"]
  ResB1R = Resistor [tolerance=±5% resistance=3.6 power=2 package=THT]
  ResR2R = Resistor [tolerance=±5% resistance=3.6 power=2 package=THT]
  ResV1R = Resistor [tolerance=±5% resistance=3.6 power=2 package=THT]
  pullDownV1T = Resistor [tolerance=±5% resistance=1k package=THT]
  pullDownR1T = Resistor [tolerance=±5% resistance=1k package=THT]
  pullDownB1T = Resistor [tolerance=±5% resistance=1k package=THT]
  pullDownR2T = Resistor [tolerance=±5% resistance=1k package=THT]
  pullDownB2T = Resistor [tolerance=±5% resistance=1k package=THT]
  36V = Power plug
  R2T = Basic FET P-Channel [package="TO220 [THT]"]
  R2 = Resistor [tolerance=±5% resistance=1k package=THT]
  Regulator_B2 = Voltage Regulator - Variable [package="TO220 [THT]"]
  Regulator_V2 = Voltage Regulator - Variable [package="TO220 [THT]"]
  Regulator_R2 = Voltage Regulator - Variable [package="TO220 [THT]"]
  Regulator_R1 = Voltage Regulator - Variable [package="TO220 [THT]"]
  Regulator_V1 = Voltage Regulator - Variable [package="TO220 [THT]"]
  Regulator_B1 = Voltage Regulator - Variable [package="TO220 [THT]"]
  pullDownV2T = Resistor [tolerance=±5% resistance=1k package=THT]
  Power_Switch = Toggle Switch [package=THT]
  PowerOnLED = female pin header, 2 pins [form="♀ (female)"]
  R3 = Resistor [tolerance=±5% resistance=6k package=THT]
  ATMega = atmega328 [package=dip]
  Clk = Resonator [frequency="16 Mhz" package=THT]
  5Vdc = male pin header, 2 pins [form="♂ (male)"]
  TransistorRes = Resistor [tolerance=±5% resistance=1k package=THT]
  TransistorRes1 = Resistor [tolerance=±5% resistance=1k package=THT]
  TransistorRes2 = Resistor [tolerance=±5% resistance=1k package=THT]
  TransistorRes3 = Resistor [tolerance=±5% resistance=1k package=THT]
  TransistorRes4 = Resistor [tolerance=±5% resistance=1k package=THT]
  TransistorRes5 = Resistor [tolerance=±5% resistance=1k package=THT]
  MIDI_IN = male pin header, 2 pins [form="♂ (male)"]
  U1 = Optocoupler [package=THT]
  C1 = Ceramic Capacitor [capacitance=100nF package="100 mil [THT, multilayer]"]
  D1 = Rectifier Diode [part_number=1N4001 package="300 mil [THT]"]
  36->5VDc = double row female pin header, 4 pins [form="♀ (female)"]
  +24V = female pin header, 1 pin [form="♀ (female)"]
  +24V_2 = female pin header, 1 pin [form="♀ (female)"]
  GND_24V = female pin header, 1 pin [form="♀ (female)"]
  U2 = RJ45 Jack [package=rj45-8]
  U3 = RJ45 Jack [package=rj45-8]
  part = Ceramic Capacitor [capacitance=100nF package="100 mil [THT, multilayer]"]  # not connected

nets:
  N1: V1T.gate, pullDownV1T.Pin_0, TransistorRes4.Pin_0
  N2: V1T.drain, ResV1R.Pin_1, Regulator_V1.ADJ
  GND: V1T.source, R1T.source, V2T.source, B2T.source, B1T.source, pullDownV1T.Pin_1, pullDownR1T.Pin_1, pullDownB1T.Pin_1, pullDownR2T.Pin_1, pullDownB2T.Pin_1, 36V.GND, R2T.source, pullDownV2T.Pin_1, PowerOnLED.pin1, ATMega.GND, Clk.GND, 5Vdc.pin1, U1.Pin_4, C1.0, 36->5VDc.pin2, 36->5VDc.pin3, GND_24V.pin1
  N3: R1T.gate, pullDownR1T.Pin_0, TransistorRes5.Pin_0
  N4: R1T.drain, ResR1R.Pin_1, Regulator_R1.ADJ
  N5: V2T.gate, pullDownV2T.Pin_0, TransistorRes1.Pin_0
  N6: V2T.drain, ResV2R.Pin_1, Regulator_V2.ADJ
  N7: ResB2R.Pin_0, Regulator_B2.OUT
  N8: ResB2R.Pin_1, B2T.drain, Regulator_B2.ADJ
  N9: ResR1R.Pin_0, Regulator_R1.OUT
  N10: ResV2R.Pin_0, Regulator_V2.OUT
  N11: B2T.gate, pullDownB2T.Pin_0, TransistorRes2.Pin_0
  N12: B1T.gate, pullDownB1T.Pin_0, TransistorRes3.Pin_0
  N13: B1T.drain, ResB1R.Pin_1, Regulator_B1.ADJ
  N14: ResB1R.Pin_0, Regulator_B1.OUT
  N15: ResR2R.Pin_0, Regulator_R2.OUT
  N16: ResR2R.Pin_1, R2T.drain, Regulator_R2.ADJ
  N17: ResV1R.Pin_0, Regulator_V1.OUT
  N18: pullDownR2T.Pin_0, R2T.gate, TransistorRes.Pin_0
  N19: 36V.VCC, Power_Switch.COM
  N20: R2.Pin_0, ATMega.D0_(RX), U1.Pin_5
  N21: R2.Pin_1, ATMega.VCC, 5Vdc.pin2, C1.1
  N22: Regulator_B2.IN, U2.2
  N23: Regulator_V2.IN, U2.4
  N24: Regulator_R2.IN, U2.6
  N25: Regulator_R1.IN, U3.6
  N26: Regulator_V1.IN, U3.4
  N27: Regulator_B1.IN, U3.2
  N28: Power_Switch.L1, R3.Pin_1, 36->5VDc.pin1, 36->5VDc.pin4, U2.1, U2.3, U3.1, U3.3
  N29: PowerOnLED.pin2, R3.Pin_0
  N30: ATMega.D3_(PWM), TransistorRes4.Pin_1
  N31: ATMega.XLAT1, Clk.0
  N32: ATMega.XLAT2, Clk.pin_1
  N33: ATMega.D5_(PWM), TransistorRes3.Pin_1
  N34: ATMega.D6_(PWM), TransistorRes5.Pin_1
  N35: ATMega.D9_(PWM), TransistorRes1.Pin_1
  N36: ATMega.D10_(PWM), TransistorRes2.Pin_1
  N37: ATMega.D11_(PWM), TransistorRes.Pin_1
  N38: MIDI_IN.pin1, U1.Pin_2, D1.anode
  N39: MIDI_IN.pin2, U1.Pin_1, D1.cathode
  N40: +24V.pin1, U2.5
  N41: +24V_2.pin1, U3.5

notes:
  B-
  R-
  B+
  V-
  PowerOnLED
  +36V
  GND
  Vcc
  R+
  V+
