# Fritzing sketch id143_Untitled_Sketch_0 (saved by Fritzing 0.9.2b)
circuit board: 3.08626cm x 2.74055cm
breadboards: 1

parts:
  VCC1 = Battery
  S1 = Pushbutton [package="[THT]"]
  LED1 = LED - 5mm [color="Red (633nm)" package="5 mm [THT]"]
  LED2 = LED - 5mm [color="Red (633nm)" package="5 mm [THT]"]
  LED3 = LED - 5mm [color="Red (633nm)" package="5 mm [THT]"]
  LED4 = LED - 5mm [color="Red (633nm)" package="5 mm [THT]"]
  LED5 = LED - 5mm [color="Red (633nm)" package="5 mm [THT]"]
  R1 = Resistor [tolerance=±5% resistance=220 package=THT]

nets:
  N1: VCC1.-, S1.Pin_4
  N2: VCC1.+, R1.Pin_0
  N3: S1.Pin_1, S1.Pin_2, LED5.cathode
  N4: LED1.cathode, LED4.anode
  N5: LED1.anode, LED2.cathode
  N6: LED2.anode, LED3.cathode
  N7: LED3.anode, R1.Pin_1
  N8: LED4.cathode, LED5.anode
