# Fritzing sketch id1442_drawdio_9v_v22_0 (saved by Fritzing 0.9.0b)
circuit board: 5.2cm x 3.2cm
breadboards: 1

parts:
  555 = IC, DIP package, 8 pins [chip_label=IC]
  Speaker = Piezo Speaker
  VCC = Battery block 9V [part_number="VCC 9V"]
  C1 = Ceramic Capacitor [capacitance=10µF package="100 mil [THT, multilayer]"]
  R1 = Resistor [tolerance=±5% resistance=300k package=THT]
  C2 = Ceramic Capacitor [capacitance=0.68nF voltage=6.3V package="100 mil [THT, multilayer]"]
  R2 = Resistor [tolerance=±5% resistance=10k package=THT]
  C3 = Ceramic Capacitor [capacitance=10nF package="100 mil [THT, multilayer]"]

nets:
  N1: 555.pin1, Speaker.pin2, VCC.-, C2.0, C3.0
  N2: 555.pin2, 555.pin6, R1.Pin_1, C2.1
  N3: 555.pin3, C1.1
  N4: 555.pin4, 555.pin8, VCC.+, R2.Pin_0
  N5: 555.pin5, C3.1
  N6: 555.pin7, R2.Pin_1
  N7: Speaker.pin1, C1.0

notes:
  nis
  -
  SND
  +
  drawdio @ Schrotty
  1
