# Fritzing sketch id1443_drawdio_0 (saved by Fritzing 0.7.11b)
breadboards: 1

parts:
  IC1 = IC, DIP package, 8 pins [chip_label=IC spacing=300mil]
  R1 = Resistor [tolerance=±5% resistance=10k package=THT]
  VCC1 = Battery
  J1 = female pin header, 2 pins [form="♀ (female)"]
  R3 = Resistor [tolerance=±5% resistance=20M package=THT]
  R4 = Resistor [tolerance=±5% resistance=10 package=THT]
  J2 = Piezo Speaker
  C1 = Ceramic Capacitor [capacitance=0.1µF package="200 mil [THT, multilayer]"]
  C2 = Ceramic Capacitor [capacitance=680pF package="200 mil [THT, multilayer]"]
  Q1 = PNP-Transistor [package="TO92 [THT]"]
  R2 = Resistor [tolerance=±5% resistance=300k package=THT]
  C3 = Electrolytic Capacitor [capacitance=100µF voltage=10V package="100 mil [THT, electrolytic]"]

nets:
  N1: IC1.pin1, VCC1.-, R3.Pin_1, R4.Pin_1, J2.pin2, C1.0, C2.0
  N2: IC1.pin2, R2.Pin_1
  N3: IC1.pin3, Q1.B
  N4: IC1.pin4, IC1.pin8, R1.Pin_0, VCC1.+, Q1.E
  N5: IC1.pin5, C1.1
  N6: IC1.pin6, R3.Pin_0, C2.1
  N7: IC1.pin7, R1.Pin_1, J1.pin1
  N8: J1.pin2, R2.Pin_0
  N9: R4.Pin_0, Q1.C, C3.+
  N10: J2.pin1, C3.-

notes:
  Rikil Shah
  Robosis
