# Fritzing sketch id1445_circuit_13_1_0 (saved by Fritzing 0.9.2b)
breadboards: 1

parts:
  부품1 = Arduino Uno (Rev3)
  LED1 = LED - 5mm [color="Red (633nm)" package="5 mm [THT]"]
  R1 = Resistor [tolerance=±5% resistance=220 package=THT]

nets:
  N1: 부품1.D13/SCK, LED1.anode
  N2: 부품1.GND, R1.Pin_0
  N3: LED1.cathode, R1.Pin_1
