# Fritzing sketch id1447_circuit_14_1_Arduino_YUN_0 (saved by Fritzing 0.9.2b)
breadboards: 1

parts:
  LED1 = LED - 5mm [color="Red (633nm)" package="5 mm [THT]"]
  R1 = Resistor [tolerance=±5% resistance=220 package=THT]
  S1 = Pushbutton [package="[THT]"]
  R2 = Resistor [tolerance=±5% resistance=10k package=THT]
  부품2 = Arduino Yun

nets:
  N1: LED1.cathode, R1.Pin_1
  N2: LED1.anode, 부품2.D13/SCK
  N3: R1.Pin_0, R2.Pin_1, 부품2.GND
  N4: S1.Pin_1, S1.Pin_2, R2.Pin_0, 부품2.D8
  N5: S1.Pin_3, S1.Pin_4, 부품2.5V
