# Fritzing sketch id1448_circuit_02_1_0 (saved by Fritzing 0.9.2b)
breadboards: 1

parts:
  부품1 = Arduino Uno (Rev3)
  BATT1 = 4xAA_Switchable_Battery_Pack_w_Bare_Wire
  J1 = Basic Servo
  J2 = Basic Servo
  J3 = Basic Servo

nets:
  N1: 부품1.D8, J3.pulse
  N2: 부품1.D9_PWM, J2.pulse
  N3: 부품1.D10_PWM/SS, J1.pulse
  GND: 부품1.GND, BATT1.connector2, J1.gnd, J2.gnd, J3.gnd
  VCC: BATT1.connector1, J1.vcc, J2.vcc, J3.vcc
