# Fritzing sketch id144_4017_Multi_LED_Blinker_0 (saved by Fritzing 0.7.10b)
breadboards: 1

parts:
  IC1 = IC, DIP package, 16 pins [chip_label="IC 4017"]
  U1 = 555 Timer [package="DIP8 [THT]"]
  VCC1 = Battery block 9V
  C1 = Electrolytic Capacitor [capacitance=10µF package="100 mil [THT, electrolytic]"]
  C2 = Ceramic Capacitor [capacitance=0.1µF package="100 mil [THT, multilayer]"]
  R1 = Trimmer Potentiometer [maximum_resistance=10kΩ package=THT]
  C3 = Ceramic Capacitor [capacitance=0.1µF package="100 mil [THT, multilayer]"]
  LED1 = LED - 5mm [color="Red (633nm)" package="5 mm [THT]"]
  LED2 = LED - 5mm [color="Red (633nm)" package="5 mm [THT]"]
  LED3 = LED - 5mm [color="Red (633nm)" package="5 mm [THT]"]
  LED4 = LED - 5mm [color="Red (633nm)" package="5 mm [THT]"]
  LED5 = LED - 5mm [color="Red (633nm)" package="5 mm [THT]"]
  LED6 = LED - 5mm [color="Red (633nm)" package="5 mm [THT]"]
  LED7 = LED - 5mm [color="Red (633nm)" package="5 mm [THT]"]
  LED8 = LED - 5mm [color="Red (633nm)" package="5 mm [THT]"]
  LED9 = LED - 5mm [color="Red (633nm)" package="5 mm [THT]"]
  LED10 = LED - 5mm [color="Red (633nm)" package="5 mm [THT]"]
  R2 = Resistor [tolerance=±5% resistance=1k package=THT]

nets:
  N1: IC1.pin1, LED6.anode
  N2: IC1.pin2, LED2.anode
  N3: IC1.pin3, LED1.anode
  N4: IC1.pin4, LED3.anode
  N5: IC1.pin5, LED7.anode
  N6: IC1.pin6, LED8.anode
  N7: IC1.pin7, LED4.anode
  N8: IC1.pin8, IC1.pin13, IC1.pin15, U1.Ground, VCC1.-, C1.-, C2.1, C3.0, R2.Pin_1
  N9: IC1.pin9, LED9.anode
  N10: IC1.pin10, LED5.anode
  N11: IC1.pin11, LED10.anode
  N12: IC1.pin14, U1.Output
  N13: IC1.pin16, U1.Vcc_Supply_Voltage, VCC1.+, R1.leg1, C3.1
  N14: U1.Trigger, U1.Threshold, C1.+, R1.leg2
  N15: U1.Control_Voltage, C2.0
  N16: U1.Discharge, R1.wiper
  N17: LED1.cathode, LED2.cathode, LED3.cathode, LED4.cathode, LED5.cathode, LED6.cathode, LED7.cathode, LED8.cathode, LED9.cathode, LED10.cathode, R2.Pin_0
