# Fritzing sketch id1450_Debounce_Switch (saved by Fritzing 0.3.10b)
breadboards: 1

parts:
  Arduino1 = Arduino
  LED1 = Red LED - 5mm
  LED3 = yellow LED - 5mm
  R1 = Resistor [resistance=220 package=THT]
  R2 = Resistor [resistance=220 package=THT]
  S1 = Pushbutton [package="[THT]"]
  R3 = Resistor [resistance=220 package=THT]

nets:
  N1: Arduino1.GND, LED1.cathode, LED3.cathode, R3.Pin_1
  N2: Arduino1.D13, R2.Pin_0
  N3: Arduino1.D12, R1.Pin_1
  N4: Arduino1.D2, S1.Pin_1, S1.Pin_2, R3.Pin_0
  N5: Arduino1.+5V, S1.Pin_3, S1.Pin_4
  N6: LED1.anode, R1.Pin_0
  N7: LED3.anode, R2.Pin_1
