# Fritzing sketch id1450_circuit_05_2_0 (saved by Fritzing 0.9.2b)
breadboards: 1

parts:
  부품1 = Arduino Uno (Rev3)
  LED1 = RGB LED (com. cathode, rgb) [package="5 mm [THT]"]

nets:
  N1: 부품1.D9_PWM, LED1.blue_anode
  N2: 부품1.D10_PWM/SS, LED1.green_anode
  N3: 부품1.D11_PWM/MOSI, LED1.common_cathode
  N4: 부품1.GND, LED1.red_anode
