# Fritzing sketch id1451_circuit_07_1_0 (saved by Fritzing 0.9.2b)
breadboards: 1

parts:
  부품1 = Arduino Uno (Rev3)
  부품2 = HC-SR04
  J1 = Basic Servo

nets:
  N1: 부품1.D9_PWM, J1.pulse
  N2: 부품1.D2, 부품2.connector9
  N3: 부품1.D3_PWM, 부품2.connector10
  5V: 부품1.5V, 부품2.connector8, J1.vcc
  GND: 부품1.GND, 부품2.connector11, J1.gnd
