# Fritzing sketch id1451_interrupt (saved by Fritzing 0.9.3b)
circuit board: 8.46667cm x 5.64444cm
breadboards: 1

parts:
  ON = Pushbutton [package="[THT]"]
  OFF = Pushbutton [package="[THT]"]
  Part1 = Arduino Uno (Rev3)

nets (from the pcb view):
  N1: ON.Pin_1, ON.Pin_2, Part1.D3_PWM
  N2: ON.Pin_3, ON.Pin_4, OFF.Pin_3, OFF.Pin_4, Part1.GND
  N3: OFF.Pin_1, OFF.Pin_2, Part1.D2
