# Fritzing sketch id1452_circuit_08_1_0 (saved by Fritzing 0.9.2b)
breadboards: 1

parts:
  부품1 = Arduino Uno (Rev3)
  J1 = Basic Servo
  J2 = Basic Servo
  LED1 = LED - 5mm [color="Red (633nm)" package="5 mm [THT]"]

nets:
  N1: 부품1.D9_PWM, J1.pulse
  N2: 부품1.D10_PWM/SS, J2.pulse
  N3: 부품1.D11_PWM/MOSI, LED1.anode
  GND: 부품1.GND, J1.gnd, J2.gnd, LED1.cathode
  VCC: 부품1.5V, J1.vcc, J2.vcc
