# Fritzing sketch id1453_circuit_09_1_0 (saved by Fritzing 0.9.2b)

parts:
  부품1 = HC-06
  부품2 = Arduino Uno (Rev3)

nets:
  N1: 부품1.connector12, 부품2.D2
  N2: 부품1.connector13, 부품2.D3_PWM
  N3: 부품1.connector14, 부품2.GND
  N4: 부품1.connector15, 부품2.5V
