# Fritzing sketch id1455_circuit_10_1_0 (saved by Fritzing 0.9.2b)
breadboards: 1

parts:
  부품1 = Arduino Uno (Rev3)
  LED1 = RGB LED (com. cathode, rgb) [package="5 mm [THT]"]
  부품2 = HC-SR04

nets:
  N1: 부품1.GND, LED1.red_anode, 부품2.connector11
  N2: 부품1.D2, 부품2.connector9
  N3: 부품1.D3_PWM, 부품2.connector10
  N4: 부품1.5V, 부품2.connector8
