# Fritzing sketch id1456_circuit_10_2_0 (saved by Fritzing 0.9.2b)
breadboards: 1

parts:
  부품1 = Arduino Uno (Rev3)
  부품2 = HC-SR04
  J1 = Piezo Speaker

nets:
  N1: 부품1.D8, J1.pin2
  N2: 부품1.GND, 부품2.connector11, J1.pin1
  N3: 부품1.D2, 부품2.connector9
  N4: 부품1.D3_PWM, 부품2.connector10
  N5: 부품1.5V, 부품2.connector8
