# Fritzing sketch id1457_circuit_11_1_0 (saved by Fritzing 0.9.2b)
breadboards: 1

parts:
  LCD1 = LCD screen
  부품1 = Arduino Uno (Rev3)
  R1 = Resistor [tolerance=±5% resistance=1k package=THT]
  R2 = Resistor [tolerance=±5% resistance=1k package=THT]
  R3 = Photocell (LDR) [package=THT]
  R4 = Resistor [tolerance=±5% resistance=10k package=THT]

nets:
  VSS: LCD1.VSS, LCD1.R/W, LCD1.LED-, 부품1.GND, R1.Pin_0, R4.Pin_1
  VDD: LCD1.VDD, 부품1.5V, R2.Pin_0, R3.pin_0
  N1: LCD1.V0, R1.Pin_1
  N2: LCD1.RS, 부품1.D12/MISO
  N3: LCD1.E, 부품1.D11_PWM/MOSI
  N4: LCD1.DB4, 부품1.D2
  N5: LCD1.DB5, 부품1.D3_PWM
  N6: LCD1.DB6, 부품1.D4
  N7: LCD1.DB7, 부품1.D5_PWM
  N8: LCD1.LED+, R2.Pin_1
  N9: 부품1.A0, R3.pin_1, R4.Pin_0
