# Fritzing sketch id1459_circuit_12_1_0 (saved by Fritzing 0.9.2b)
breadboards: 1

parts:
  부품1 = Arduino Uno (Rev3)
  DI1 = 7-Segment LED Display [package=THT]
  R1 = Resistor [tolerance=±20% resistance=220 package=THT]

nets:
  N1: 부품1.D8, DI1.cathodeG
  N2: 부품1.D9_PWM, DI1.cathodeDP
  N3: 부품1.D2, DI1.cathodeA
  N4: 부품1.D3_PWM, DI1.cathodeB
  N5: 부품1.D4, DI1.cathodeC
  N6: 부품1.D5_PWM, DI1.cathodeD
  N7: 부품1.D6_PWM, DI1.cathodeE
  N8: 부품1.D7, DI1.cathodeF
  N9: 부품1.5V, R1.Pin_0
  N10: DI1.commAnode#2, R1.Pin_1
