# Fritzing sketch id145_555_ASTABLE_0 (saved by Fritzing 0.9.0b)
breadboards: 1

parts:
  U1 = 555 Timer [package="DIP8 [THT]"]
  C1 = Electrolytic Capacitor [capacitance=1µF package="100 mil [THT, electrolytic]"]
  R1 = Resistor [tolerance=±5% resistance=10k package=THT]
  R2 = Rotary Potentiometer (Large) [maximum_resistance=100kΩ package=THT]
  LED1 = LED - 5mm [color="Red (633nm)" package="5 mm [THT]"]
  R3 = Resistor [tolerance=±5% resistance=220 package=THT]

nets:
  GND: U1.Ground, C1.-, R3.Pin_1
  N1: U1.Trigger, U1.Threshold, C1.+, R2.wiper
  N2: U1.Output, LED1.anode
  12V: U1.Reset, U1.Vcc_Supply_Voltage, R1.Pin_0
  N3: U1.Discharge, R1.Pin_1, R2.leg1
  N4: LED1.cathode, R3.Pin_0
