# Fritzing sketch id1460_circuit_12_2_0 (saved by Fritzing 0.9.2b)
breadboards: 1

parts:
  부품1 = Arduino Uno (Rev3)
  DI1 = 7-Segment LED Display [package=THT]
  R1 = Resistor [tolerance=±20% resistance=220 package=THT]
  R2 = Resistor [tolerance=±5% resistance=10k package=THT]
  S1 = Pushbutton [package="[THT]"]
  R3 = Resistor [tolerance=±5% resistance=10k package=THT]
  S2 = Pushbutton [package="[THT]"]

nets:
  N1: 부품1.D8, DI1.cathodeG
  N2: 부품1.D9_PWM, DI1.cathodeDP
  N3: 부품1.D11_PWM/MOSI, R3.Pin_1, S2.Pin_3, S2.Pin_4
  N4: 부품1.D12/MISO, R2.Pin_1, S1.Pin_3, S1.Pin_4
  N5: 부품1.D2, DI1.cathodeA
  N6: 부품1.D3_PWM, DI1.cathodeB
  N7: 부품1.D4, DI1.cathodeC
  N8: 부품1.D5_PWM, DI1.cathodeD
  N9: 부품1.D6_PWM, DI1.cathodeE
  N10: 부품1.D7, DI1.cathodeF
  N11: 부품1.5V, R1.Pin_0, S1.Pin_1, S1.Pin_2, S2.Pin_1, S2.Pin_2
  N12: 부품1.GND, R2.Pin_0, R3.Pin_0
  N13: DI1.commAnode#2, R1.Pin_1
