# Fritzing sketch id1462_circuit_13_2_0 (saved by Fritzing 0.9.2b)
breadboards: 1

parts:
  부품1 = Arduino Uno (Rev3)
  J1 = Basic Servo
  R1 = Rotary Potentiometer (Large) [maximum_resistance=100kΩ package=THT]

nets:
  N1: 부품1.A0, R1.wiper
  N2: 부품1.D9_PWM, J1.pulse
  5V: 부품1.5V, J1.vcc, R1.leg2
  GND: 부품1.GND, J1.gnd, R1.leg1
