# Fritzing sketch id1463_circuit_4_3_0 (saved by Fritzing 0.9.1b)
breadboards: 1

parts:
  부품1 = Arduino Uno (Rev3)
  R1 = Resistor [tolerance=±5% resistance=10k package=THT]
  S1 = Pushbutton [package="[THT]"]

nets:
  N1: 부품1.D13/SCK, R1.Pin_1, S1.Pin_3, S1.Pin_4
  N2: 부품1.GND, R1.Pin_0
  N3: 부품1.5V, S1.Pin_1, S1.Pin_2
