# Fritzing sketch id146_Untitled_Sketch_0 (saved by Fritzing 0.8.5b)
breadboards: 1

parts:
  U1 = 555 Timer [package="SO8 [SMD]"]
  Part1 = Arduino Uno (Rev3)
  C1 = Electrolytic Capacitor [capacitance=10µF package="100 mil [THT, electrolytic]"]
  R2 = Resistor [tolerance=±5% resistance=22k package=THT]
  C2 = Ceramic Capacitor [capacitance=10nF package="100 mil [THT, multilayer]"]
  LED1 = LED - 5mm [color="Red (633nm)" package="5 mm [THT]"]
  R3 = Resistor [tolerance=±5% resistance=220 package=THT]
  R1 = Resistor [tolerance=±5% resistance=100k package=THT]

nets:
  N1: U1.Pin_1, Part1.GND, C1.-, C2.1, R3.Pin_1
  N2: U1.Pin_2, U1.Pin_6, C1.+, R2.Pin_0
  N3: U1.Pin_3, LED1.anode
  N4: U1.Pin_4, U1.Pin_8, Part1.5V, R1.Pin_0
  N5: U1.Pin_5, C2.0
  N6: U1.Pin_7, R2.Pin_1, R1.Pin_1
  N7: LED1.cathode, R3.Pin_0
