# Fritzing sketch id1472_circuit_8_2_0 (saved by Fritzing 0.9.2b)
breadboards: 1

parts:
  부품1 = Arduino Uno (Rev3)
  S1 = Pushbutton [package="[THT]"]
  R1 = Resistor [tolerance=±5% resistance=10k package=THT]
  S2 = Pushbutton [package="[THT]"]
  R2 = Resistor [tolerance=±5% resistance=10k package=THT]
  S3 = Pushbutton [package="[THT]"]
  R3 = Resistor [tolerance=±5% resistance=10k package=THT]
  J1 = Piezo Speaker

nets:
  N1: 부품1.D8, J1.pin2
  N2: 부품1.D2, S1.Pin_3, S1.Pin_4, R1.Pin_1
  N3: 부품1.D3_PWM, S2.Pin_3, S2.Pin_4, R2.Pin_1
  N4: 부품1.D4, S3.Pin_3, S3.Pin_4, R3.Pin_1
  N5: 부품1.5V, S1.Pin_1, S1.Pin_2, S2.Pin_1, S2.Pin_2, S3.Pin_1, S3.Pin_2
  N6: 부품1.GND, R1.Pin_0, R2.Pin_0, R3.Pin_0, J1.pin1
