# Fritzing sketch id1474_circuit_9_2_0 (saved by Fritzing 0.9.2b)
breadboards: 1

parts:
  부품1 = Arduino Uno (Rev3)
  R2 = Resistor [tolerance=±5% resistance=10k package=THT]
  R3 = Photocell (LDR) [package=THT]
  J1 = Piezo Speaker

nets:
  N1: 부품1.A0, R2.Pin_0, R3.pin_1
  N2: 부품1.D8, J1.pin2
  N3: 부품1.GND, R2.Pin_1, J1.pin1
  N4: 부품1.5V, R3.pin_0
