# Fritzing sketch id1475_circuit5_1_0 (saved by Fritzing 0.9.3b)
breadboards: 1

parts:
  Raspberry_Pi_1 = Raspberry Pi 3 [part_number=RPI-3-V1.2]
  R1 = Resistor [tolerance=±5% resistance=220 package=THT]
  LED1 = LED - 5mm [color="Red (633nm)" package="5 mm [THT]"]

nets:
  N1: Raspberry_Pi_1.GPIO17, R1.Pin_1
  N2: Raspberry_Pi_1.GND, LED1.cathode
  N3: R1.Pin_0, LED1.anode
