# Fritzing sketch id1478_L293D_0 (saved by Fritzing 0.7.9b)
breadboards: 1

parts:
  IC1 = L293D [package=THT]
  M1 = DC Motor
  Arduino1 = Arduino
  part = Battery  # not connected
  VCC1 = 4 x AAA Battery Mount
  R1 = 1k Ω Resistor [package=THT]
  R2 = 1k Ω Resistor [package=THT]
  part_2 = Trimmer Potentiometer [maximum_resistance=10kΩ package=THT]  # not connected
  part_3 = Rotary Potentiometer (Large) [maximum_resistance=100kΩ package=THT]  # not connected
  part_4 = Rotary Potentiometer (Small)  # not connected
  R4 = Rotary Potentiometer (Large) [package=THT]

nets:
  N1: IC1.Enable_1, Arduino1.D3
  N2: IC1.In_1, R1.Pin_1
  N3: IC1.Out_1_(_Controlled_by_Enable_1_), M1.pin_1
  GND: IC1.0V, Arduino1.GND, VCC1.-, R2.Pin_1, R4.leg1
  N4: IC1.In_2, R2.Pin_0
  N5: IC1.+Vmotor, VCC1.+
  5V: IC1.+V, Arduino1.+5V, R1.Pin_0, R4.leg2
  N6: Arduino1.A0, R4.wiper
