# Fritzing sketch id147_FritzingBeepGame_0 (saved by Fritzing 0.6.4b)
breadboards: 1

parts:
  SPKR1 = Loudspeaker
  VCC1 = Battery block 9V
  J1 = female pin header, 1 pin [form="♀ (female)"]
  J2 = female pin header, 1 pin [form="♀ (female)"]
  IC200 = 555 Timer [package="SO8 [SMD]"]
  R217 = Resistor [tolerance=±5% resistance=33k package="1206 [SMD]"]
  R228 = Resistor [tolerance=±5% resistance=1k package="1206 [SMD]"]
  R216 = Resistor [tolerance=±5% resistance=33k package="1206 [SMD]"]
  R214 = Resistor [tolerance=±5% resistance=4.7k package="1206 [SMD]"]
  C212 = Ceramic Capacitor [capacitance=100nF package="1206 [SMD, multilayer]"]
  C1 = Electrolytic Capacitor [capacitance=1µF package="100 mil [THT, electrolytic]"]
  C281 = Ceramic Capacitor [capacitance=100nF package="1206 [SMD, multilayer]"]
  C231 = Electrolytic Capacitor [capacitance=1µF package="100 mil [THT, electrolytic]"]
  R1 = Resistor [tolerance=±5% resistance=470 package="1206 [SMD]"]
  LED1 = smd LED [color="Red (633nm)" package="1206 [SMD]"]

nets:
  GND: SPKR1.pin1, VCC1.-, IC200.Pin_1, R214.Pin_1, C212.1, C1.-, C281.0, LED1.cathode
  N1: SPKR1.pin2, C231.-
  N2: VCC1.+, IC200.Pin_8, R217.Pin_0, R228.Pin_0, C1.+, C281.1, R1.Pin_1
  N3: J1.pin1, R228.Pin_1
  N4: J2.pin1, IC200.Pin_4, R214.Pin_0
  N5: IC200.Pin_2, IC200.Pin_6, R216.Pin_1, C212.0
  N6: IC200.Pin_3, C231.+
  N7: IC200.Pin_7, R217.Pin_1, R216.Pin_0
  N8: R1.Pin_0, LED1.anode

notes:
  Calculation of the frequency.
  For R117=R116 you can use:
  1
  f = ---------------------------
  2.1 * C212 * R217
  For detail signal pulse pause differentiation use:
  1 1
  f= ------------------------------ = ---------------
  (timpulse + tpause) ( ti + tp )
  ti= 0.7 * C212 * R217+R216
  tp=0.7 * C212 * R216
  Detailed calculation for this example:
  1 1
  f = ------------------------------------- = -------------------------------
  0.7 * C212(R217+2*R216) 0.7* 10nF(33k+66k)
  1 1
  = -------------------------------------- = --------------------- = 1443 Hz
  0,000007F* 66000 Ohm 0.462 sec
  Schematic shows a beep game you can test your steady hand.
  Connection between wire aberration and play stick will cause a beep.
  R228 is for short circuit protection!!!
  Schematic shows a beep game you can test your steady hand.
  Leave this area free from other power signals to avoid short circuit connection!
  555 Tutorial, Beep Game with a resetcontrolled 555 generator, 2
  Beep Game
  555 Tutorial
