# Fritzing sketch id1480_tuto_driver_cc_0 (saved by Fritzing 0.9.3b)

parts:
  U1 = LIPO-2000mAh [package=lipo-2000]
  Composant1 = Arduino Uno (Rev3)
  Composant2 = Arduino Motor Shield (Rev3)
  M1 = DC Motor

nets:
  N1: U1.+, Composant2.VMOT
  GND: U1.-, Composant1.GND, Composant2.GND
  N2: Composant1.D11_PWM/MOSI, Composant2.D11_PWM/B
  N3: Composant1.D13/SCK, Composant2.D13/DirB
  N4: Composant2.B-, M1.pin_2
  N5: Composant2.B+, M1.pin_1
