# Fritzing sketch id1481_Driver_motor_de_passo_0 (saved by Fritzing 0.7.12b)
breadboards: 1

parts:
  Da = Rectifier Diode [part_number=1N4004 package="300 mil [THT]"]
  Db = Rectifier Diode [part_number=1N4004 package="300 mil [THT]"]
  Qd = npn-Powertransistor [part_number=TIP41C package="TO220 [THT]"]
  Qb = npn-Powertransistor [part_number=TIP41C package="TO220 [THT]"]
  Qc = npn-Powertransistor [part_number=TIP41C package="TO220 [THT]"]
  Rd = Resistor [tolerance=±5% resistance=220 package=THT]
  Rc = Resistor [tolerance=±5% resistance=220 package=THT]
  Dc = Rectifier Diode [part_number=1N4001 package="300 mil [THT]"]
  Power = Power plug
  GND = female pin header, 1 pin [form="♀ (female)"]
  Dd = Rectifier Diode [part_number=1N4004 package="300 mil [THT]"]
  Rb = Resistor [tolerance=±5% resistance=220 package=THT]
  J1 = female pin header, 4 pins [form="♀ (female)"]
  Qa = npn-Powertransistor [part_number=TIP41C package="TO220 [THT]"]
  Ra = Resistor [tolerance=±5% resistance=220 package=THT]
  Motor = screw terminal, 6 pins

nets:
  N1: Da.cathode, Qa.collector, Motor.pin3
  N2: Da.anode, Db.anode, Qd.emitter, Qb.emitter, Qc.emitter, Dc.anode, Power.GND, GND.pin1, Dd.anode, Qa.emitter
  N3: Db.cathode, Qb.collector, Motor.pin4
  N4: Qd.base, Rd.Pin_0
  N5: Qd.collector, Dd.cathode, Motor.pin6
  N6: Qb.base, Rb.Pin_0
  N7: Qc.base, Rc.Pin_0
  N8: Qc.collector, Dc.cathode, Motor.pin5
  N9: Rd.Pin_1, J1.pin4
  N10: Rc.Pin_1, J1.pin3
  N11: Power.VCC, Motor.pin1, Motor.pin2
  N12: Rb.Pin_1, J1.pin2
  N13: J1.pin1, Ra.Pin_1
  N14: Qa.base, Ra.Pin_0

notes:
  Motor
  Power
  Arduino
  d c b a + +
