# Fritzing sketch id1484_carrera_DriverDisplay_mit_Nextion_3,2_87o5IdJ_0 (saved by Fritzing 0.9.3b)
breadboards: 1

parts:
  R1 = Resistor [tolerance=±5% resistance=22k package=THT]
  D1 = Rectifier Diode [part_number=1N4001 package="300 mil [THT]"]
  R2 = Resistor [tolerance=±5% resistance=8.2k package=THT]
  Bauteil1 = Arduino Nano (Rev3.0)
  Carrera_Controll_Unit_1 = Carrera_Controll_Unit_30352 [part_number=20030352]
  U3 = Nokia 6100 Color LCD [package=nokia6100_lcd]
  X1 = USB Connectors [package=usb-a-pcb]

nets (from the breadboard view):
  N1: R1.Pin_0, D1.cathode
  N2: R1.Pin_1, R2.Pin_0, Bauteil1.D2, Bauteil1.D3
  N3: D1.anode, Carrera_Controll_Unit_1.connector2
  N4: R2.Pin_1, Bauteil1.D0/RX, Bauteil1.RESET, Bauteil1.GND, Carrera_Controll_Unit_1.connector7, U3.VDIGITAL, U3.DIO, X1.D-
  N5: Bauteil1.D1/TX, U3.RESET
  N6: Bauteil1.5V, X1.D+
  N7: U3.SCK, U3.CS, X1.VBUS

notes:
  NX4024T032_011
  NEXTION 3,2"
