# Fritzing sketch id1486_DRO_0 (saved by Fritzing 0.9.3b)
circuit board: 8.46667cm x 5.64444cm
breadboards: 2

parts:
  LCD1 = LCD screen
  R1 = Rotary Potentiometer (Small) [maximum_resistance=10kΩ package=THT]
  Composant1 = Arduino Nano (Rev3.0)
  Q1 = NPN-Transistor [package="TO92 [THT]"]
  Q2 = NPN-Transistor [package="TO92 [THT]"]
  R3 = Resistor [tolerance=±5% resistance=10k package=THT]
  R5 = Resistor [tolerance=±5% resistance=10k package=THT]
  Q3 = NPN-Transistor [package="TO92 [THT]"]
  Q4 = NPN-Transistor [package="TO92 [THT]"]
  PACX = female pin header, 4 pins [form="♀ (female)"]
  Q5 = NPN-Transistor [package="TO92 [THT]"]
  Q6 = NPN-Transistor [package="TO92 [THT]"]
  R15 = Resistor [tolerance=±5% resistance=10k package=THT]
  R17 = Resistor [tolerance=±5% resistance=10k package=THT]
  R20 = Resistor [tolerance=±5% resistance=10k package=THT]
  R21 = Resistor [tolerance=±5% resistance=10k package=THT]
  PACY = female pin header, 4 pins [form="♀ (female)"]
  PACZ = female pin header, 4 pins [form="♀ (female)"]
  R22 = Resistor [tolerance=±5% resistance=10k package=THT]
  R23 = Resistor [tolerance=±5% resistance=10k package=THT]

nets:
  VSS: LCD1.VSS, LCD1.R/W, R1.leg2, Composant1.GND, Q1.E, Q2.E, Q3.E, Q4.E, PACX.pin4, Q5.E, Q6.E, PACY.pin4, PACZ.pin4, R22.Pin_0
  VDD: LCD1.VDD, R1.leg1, Composant1.5V
  N1: LCD1.V0, R1.wiper
  N2: LCD1.RS, Composant1.D6
  N3: LCD1.E, Composant1.D5
  N4: LCD1.DB3, Composant1.D4
  N5: LCD1.DB4, Composant1.D3
  N6: LCD1.DB5, Composant1.D2
  N7: LCD1.DB6, Composant1.D1/TX
  N8: Composant1.D7, Q1.C
  N9: Composant1.D8, Q2.C
  N10: Composant1.D9, Q3.C
  N11: Composant1.D10, Q4.C
  N12: Composant1.D11/MOSI, Q5.C
  N13: Composant1.D12/MISO, Q6.C
  N14: Composant1.3V3, R23.Pin_1
  N15: Q1.B, R3.Pin_1
  N16: Q2.B, R5.Pin_1
  N17: R3.Pin_0, PACZ.pin3
  N18: R5.Pin_0, PACZ.pin2
  N19: Q3.B, R15.Pin_1
  N20: Q4.B, R17.Pin_1
  N21: PACX.pin1, PACY.pin1, PACZ.pin1, R22.Pin_1, R23.Pin_0
  N22: PACX.pin2, R21.Pin_0
  N23: PACX.pin3, R20.Pin_0
  N24: Q5.B, R20.Pin_1
  N25: Q6.B, R21.Pin_1
  N26: R15.Pin_0, PACY.pin3
  N27: R17.Pin_0, PACY.pin2

notes:
  PACZ
  Ordre connecteur PAC  : VCC CLK SDA GND
  PACY
  PACX
  Alimentation des PACS
