# Fritzing sketch id1487_DROPCAR_AUTO_JUDGE_20180125_0858_0 (saved by Fritzing 0.9.3b)
breadboards: 1

parts:
  Part1 = Arduino Uno (Rev3)
  S1_LANE1 = Pushbutton [package="[THT]"]
  S2_LANE_2 = Pushbutton [package="[THT]"]
  S3_LANE_3 = Pushbutton [package="[THT]"]
  S4_LANE_4 = Pushbutton [package="[THT]"]
  R1 = Resistor [tolerance=±5% resistance=270 package=THT]
  R2 = Resistor [tolerance=±5% resistance=270 package=THT]
  R4 = Resistor [tolerance=±5% resistance=270 package=THT]
  S5_START = Pushbutton [package="[THT]"]
  S6_RESET = Pushbutton [package="[THT]"]
  LANE_1 = LED - 5mm [color="Red (633nm)" package="5 mm [THT]"]
  LANE_2 = LED - 5mm [color="Red (633nm)" package="5 mm [THT]"]
  LANE_3 = LED - 5mm [color="Red (633nm)" package="5 mm [THT]"]
  LANE_4 = LED - 5mm [color="Red (633nm)" package="5 mm [THT]"]
  START = LED - 5mm [color="Green (570nm)" package="5 mm [THT]"]
  RESET = LED - 5mm [color="Yellow (595nm)" package="5 mm [THT]"]
  R3 = Resistor [tolerance=±5% resistance=270 package=THT]
  U1 = 74HC595 [package="DIP16 [THT]"]
  R5 = Resistor [tolerance=±5% resistance=270 package=THT]
  R6 = Resistor [tolerance=±5% resistance=270 package=THT]
  J1 = Basic Servo
  Part2 = adafruit [part_number=878]

nets:
  N1: Part1.D8, S1_LANE1.Pin_3, S1_LANE1.Pin_4
  N2: Part1.D9_PWM, S2_LANE_2.Pin_3, S2_LANE_2.Pin_4
  N3: Part1.D10_PWM/SS, S3_LANE_3.Pin_3, S3_LANE_3.Pin_4
  N4: Part1.D11_PWM/MOSI, S4_LANE_4.Pin_3, S4_LANE_4.Pin_4
  N5: Part1.D12/MISO, S5_START.Pin_3, S5_START.Pin_4
  N6: Part1.D13/SCK, S6_RESET.Pin_3, S6_RESET.Pin_4
  GND: Part1.GND, S1_LANE1.Pin_1, S1_LANE1.Pin_2, S2_LANE_2.Pin_1, S2_LANE_2.Pin_2, S3_LANE_3.Pin_1, S3_LANE_3.Pin_2, S4_LANE_4.Pin_1, S4_LANE_4.Pin_2, S5_START.Pin_1, S5_START.Pin_2, S6_RESET.Pin_1, S6_RESET.Pin_2, LANE_1.cathode, LANE_2.cathode, LANE_3.cathode, LANE_4.cathode, START.cathode, RESET.cathode, J1.gnd, Part2.connector7
  N7: Part1.D2, Part2.connector5
  N8: Part1.D3_PWM, Part2.connector6
  N9: Part1.D4, J1.pulse
  N10: Part1.D5_PWM, U1.DS
  N11: Part1.D6_PWM, U1.ST_CP
  N12: Part1.D7, U1.SH_CP
  VCC: Part1.5V, U1.VCC, J1.vcc, Part2.connector8
  N13: R1.Pin_0, U1.Q0
  N14: R1.Pin_1, LANE_1.anode
  N15: R2.Pin_0, U1.Q1
  N16: R2.Pin_1, LANE_2.anode
  N17: R4.Pin_0, U1.Q3
  N18: R4.Pin_1, LANE_4.anode
  N19: LANE_3.anode, R3.Pin_1
  N20: START.anode, R5.Pin_0
  N21: RESET.anode, R6.Pin_0
  N22: R3.Pin_0, U1.Q2
  N23: U1.Q4, R5.Pin_1
  N24: U1.Q5, R6.Pin_1
