# Fritzing sketch id1488_drumvest_0 (saved by Fritzing 0.8.3b)
circuit board: 16.9333cm x 5.64444cm

parts:
  Xbee = LilyPad XBee
  LiPo = LIPO-2000mAh [package=lipo-2000]
  Sensitivity_Pot = TRIMPOT [package=3362u-2]
  Pressure_Sensor = Textile Analog Pressure Sensor [part_number=PW073]
  Female = Header 2 [package=jst-2-smd]
  Male = Header 2 [package=jst-2-smd]

nets:
  N1: Xbee.3.3V, Female.2
  N2: Xbee.GND, Sensitivity_Pot.CCW, Sensitivity_Pot.WIPER, Female.1
  N3: Xbee.D0, Sensitivity_Pot.CW, Pressure_Sensor.pin_0
  N4: Xbee.VCC, Xbee.VREF, Pressure_Sensor.pin_1
  N5: LiPo.+, Male.2
  N6: LiPo.-, Male.1
