# Fritzing sketch id148_LM555_DualLedFlasher_0 (saved by Fritzing 0.7.10b)
breadboards: 1

parts:
  R3 = Resistor [tolerance=±5% resistance=220 package=THT]
  LED4 = LED - 3mm [color="Green (570nm)" package="3 mm [THT]"]
  U1 = 555 Timer [part_number=LM555 package="DIP8 [THT]"]
  LED5 = LED - 3mm [color="Red (660nm)" package="3 mm [THT]"]
  R4 = Resistor [tolerance=±5% resistance=220 package=THT]
  R2 = Resistor [tolerance=±5% resistance=4.7k package=THT]
  R1 = Resistor [tolerance=±5% resistance=4.7k package=THT]
  C1 = Electrolytic Capacitor [capacitance=1µF voltage=16V package="100 mil [THT, electrolytic]"]
  VCC1 = Battery block 9V

nets:
  N1: R3.Pin_0, U1.Output, R4.Pin_0
  N2: R3.Pin_1, LED4.cathode
  N3: LED4.anode, U1.Reset, U1.Vcc_Supply_Voltage, R1.Pin_0, VCC1.+
  N4: U1.Ground, LED5.cathode, C1.-, VCC1.-
  N5: U1.Trigger, U1.Threshold, R2.Pin_1, C1.+
  N6: U1.Discharge, R2.Pin_0, R1.Pin_1
  N7: LED5.anode, R4.Pin_1
