# Fritzing sketch id1490_Reloj_0 (saved by Fritzing 0.9.0b)
circuit board: 11.3357cm x 6.68587cm
breadboards: 1

parts:
  LED5 = LED - 5mm [color="Red (633nm)" package="5 mm [THT]"]
  LED6 = LED - 5mm [color="Red (633nm)" package="5 mm [THT]"]
  LED7 = LED - 5mm [color="Red (633nm)" package="5 mm [THT]"]
  LED8 = LED - 5mm [color="Red (633nm)" package="5 mm [THT]"]
  LED9 = LED - 5mm [color="Red (633nm)" package="5 mm [THT]"]
  LED10 = LED - 5mm [color="Red (633nm)" package="5 mm [THT]"]
  R1 = Resistor [tolerance=±5% resistance=220 package=THT]
  Parte1 = Arduino Mega ADK (Rev3)
  S1 = Pushbutton [package=THT]
  R3 = Resistor [tolerance=±5% resistance=220 package=THT]
  LED14 = LED - 5mm [color="Red (633nm)" package="5 mm [THT]"]
  LED15 = LED - 5mm [color="Red (633nm)" package="5 mm [THT]"]
  LED16 = LED - 5mm [color="Red (633nm)" package="5 mm [THT]"]
  LED17 = LED - 5mm [color="Red (633nm)" package="5 mm [THT]"]
  LED18 = LED - 5mm [color="Red (633nm)" package="5 mm [THT]"]
  LED19 = LED - 5mm [color="Red (633nm)" package="5 mm [THT]"]
  LED20 = LED - 5mm [color="Red (633nm)" package="5 mm [THT]"]
  R4 = Resistor [tolerance=±5% resistance=220 package=THT]
  JP2 = Header 4 [package=molex-1x4_lock]

nets:
  N1: LED5.cathode, LED6.cathode, LED7.cathode, LED8.cathode, LED9.cathode, LED10.cathode, R1.Pin_0, LED18.cathode
  N2: LED5.anode, Parte1.D2_PWM
  N3: LED6.anode, Parte1.D4_PWM
  N4: LED7.anode, Parte1.D5_PWM
  N5: LED8.anode, Parte1.D6_PWM
  N6: LED9.anode, Parte1.D7_PWM
  N7: LED10.anode, Parte1.D8_PWM
  N8: R1.Pin_1, Parte1.GND, S1.leg0, R3.Pin_0, R4.Pin_1, JP2.1
  N9: Parte1.A0, LED14.anode
  N10: Parte1.A1, LED15.anode
  N11: Parte1.A2, LED16.anode
  N12: Parte1.A3, LED17.anode
  N13: Parte1.A4, LED19.anode
  N14: Parte1.A5, LED20.anode
  N15: Parte1.D21/SCL, JP2.4
  N16: Parte1.D20/SDA, JP2.3
  N17: Parte1.D9_PWM, LED18.anode
  N18: Parte1.D3_PWM, S1.leg1
  N19: Parte1.5V, JP2.2
  N20: R3.Pin_1, LED14.cathode, LED15.cathode, LED16.cathode, LED17.cathode
  N21: LED19.cathode, LED20.cathode, R4.Pin_0

notes:
  1
  2
  4
  8
  16
  32
  seg
  pm
  am
  scl
  sda
  vcc
  gnd
