# Fritzing sketch id1491_Era_RTC_v.0.4_0 (saved by Fritzing 0.9.3b)
circuit board: 3.55cm x 2.8cm
breadboards: 1

parts:
  CR2032 = Battery Holders [package=battcom_20mm_pth]
  DS1307 = DS1307 [package=THT]
  J1 = female pin header, 5 pins [form="♀ (female)"]
  32_768 = CRYSTAL [package=tc26h]
  1K = Resistor [tolerance=±5% resistance=220 package=THT]
  1K_2 = Resistor [tolerance=±5% resistance=220 package=THT]
  1K_3 = Resistor [tolerance=±5% resistance=220 package=THT]
  C1 = Ceramic Capacitor [capacitance=100nF package="200 mil [THT, multilayer]"]

nets:
  N1: CR2032.+, DS1307.Vbat_-_Backup_Supply
  N2: CR2032.-, DS1307.0V, J1.pin5, C1.0
  N3: DS1307.X1_-_Crystal, 32_768.2
  N4: DS1307.X2_-_Crystal, 32_768.1
  N5: DS1307.SDA_-_I2C_Data, J1.pin4, 1K_2.Pin_1
  N6: DS1307.SCL_-_I2C_Clock, J1.pin3, 1K.Pin_1
  N7: DS1307.SWQ/OUT_-_Clock_Output, J1.pin2, 1K_3.Pin_0
  N8: DS1307.+V, J1.pin1, 1K.Pin_0, 1K_2.Pin_0, 1K_3.Pin_1, C1.1

notes:
  EraLabs
  DS1307 RTC Module
  vcc
  gnd
  scl
  sda
  v.0.4
  swq
