# Fritzing sketch id1492_templcd_0 (saved by Fritzing 0.7.10b)
breadboards: 1

parts:
  Arduino1 = Arduino
  LCD1 = LCD screen
  T1 = LM34 Temperature Sensor [thermistor_type=NTC part_number=ds18b20 package="TO92 [THT]"]
  R2 = Resistor [tolerance=±5% resistance=470 package=THT]
  R3 = Rotary Potentiometer (Small) [maximum_resistance=100kΩ]

nets:
  GND: Arduino1.GND, LCD1.VSS, LCD1.R/W, LCD1.LED-, T1.+Vs, R3.leg1
  N1: Arduino1.D12, LCD1.RS
  N2: Arduino1.D11, LCD1.E
  N3: Arduino1.D7, T1.Vout, R2.Pin_0
  N4: Arduino1.D5, LCD1.DB4
  N5: Arduino1.D4, LCD1.DB5
  N6: Arduino1.D3, LCD1.DB6
  N7: Arduino1.D2, LCD1.DB7
  +5V: Arduino1.+5V, LCD1.VDD, LCD1.LED+
  N8: LCD1.V0, R3.wiper
  N9: T1.GND, R2.Pin_1

notes:
  DS18B20 Temp sensor
  10K Potention meter
  470ohm resistor
  i have 16x2 LCD but this code for 20x4 but is working
  http://www.x-firm.com/processing/Blog/LCD.pde
