# Fritzing sketch id1493_Untitled_Sketch_2_0 (saved by Fritzing 0.9.2b)
breadboards: 1

parts:
  R1 = Resistor [tolerance=±5% resistance=220 package=THT]
  LED1 = LED - 5mm [color="Red (633nm)" package="5 mm [THT]"]
  MIC1 = Microphone
  SPKR1 = Loudspeaker
  Bauteil1 = pinocc.io scout  # not connected

nets:
  N1: R1.Pin_0, MIC1.pin1, SPKR1.pin1
  N2: R1.Pin_1, LED1.cathode
  5V: LED1.anode
  N3: MIC1.pin2, SPKR1.pin2
