# Fritzing sketch id1494_pupil_LED_0 (saved by Fritzing 0.9.1b)
breadboards: 1

parts:
  R1 = Resistor [tolerance=±5% resistance=220 package=THT]
  LED1 = LED - 3mm [color="Green (555nm)" package="3 mm [THT]"]
  LED2 = LED - 3mm [color="Red (633nm)" package="3 mm [THT]"]
  LED3 = LED - 3mm [color="Orange (605nm)" package="3 mm [THT]"]
  Componente1 = Arduino Mega 2560 (Rev3)

nets:
  N1: R1.Pin_0, Componente1.GND
  N2: R1.Pin_1, LED1.cathode, LED2.cathode, LED3.cathode
  N3: LED1.anode, Componente1.D12_PWM
  N4: LED2.anode, Componente1.D6_PWM
  N5: LED3.anode, Componente1.D2_PWM
