# Fritzing sketch id1496_DSLR_Slide_Scanner_0 (saved by Fritzing 0.8.7b)
circuit board: 16.9333cm x 5.64444cm
breadboards: 2

parts:
  D1 = Rectifier Diode [part_number=1N4001 package="300 mil [THT]"]
  IC1 = Voltage Regulator [part_number=7805 package=78xxl]
  C1 = Electrolytic Capacitor [capacitance=0.1mF voltage=50V package="100 mil [THT, electrolytic]"]
  C2 = Electrolytic Capacitor [capacitance=10µF package="100 mil [THT, electrolytic]"]
  J1 = Power Jack [package=power_jack_combo]
  LED1 = LED - 5mm [color="Red (660nm)" part_number=OPERATION package="5 mm [THT]"]
  U1 = atmega328 [package=dip]
  R1 = Resistor [tolerance=±5% resistance=220 package=THT]
  XTAL1 = Crystal [frequency="16 Mhz" package=THT]
  R2 = Resistor [tolerance=±5% resistance=10k package=THT]
  C5 = Ceramic Capacitor [capacitance=100nF package="100 mil [THT, multilayer]"]
  C6 = Ceramic Capacitor [capacitance=22pF package="100 mil [THT, multilayer]"]
  F1 = Resettable Fuse PTC [package=ptc]
  LED2 = LED - 5mm [color="Blue (505nm)" part_number=STATUS package="5 mm [THT]"]
  R3 = Resistor [tolerance=±5% resistance=10k package=THT]
  S1 = Toggle Switch [package=THT]
  C3 = Ceramic Capacitor [capacitance=22pF package="100 mil [THT, multilayer]"]
  S2 = Pushbutton [part_number=Start/Pause package="[THT]"]
  R6 = Resistor [tolerance=±5% resistance=10k package=THT]
  D2 = Rectifier Diode [part_number=1N4001 package="300 mil [THT]"]
  R8 = Resistor [tolerance=±5% resistance=1k package=THT]
  R9 = Resistor [tolerance=±5% resistance=10k package=THT]
  Q1 = NPN-Transistor [part_number=2N3904 package="TO92 [THT]"]
  U3 = 3.5mm Audio Jack [package=audio-jack]
  U2 = RELAY-2 [package=relay-g5v]
  U4 = Optocoupler [package=THT]
  LED4 = LED - 5mm [color="Green (560nm)" part_number=SHUTTER package="5 mm [THT]"]
  R10 = Resistor [tolerance=±5% resistance=560 package=THT]
  LED5 = LED - 5mm [color="Orange (620nm)" part_number=FOCUS package="5 mm [THT]"]
  R11 = Resistor [tolerance=±5% resistance=560 package=THT]
  U5 = Optocoupler [package=THT]
  U6 = 3.5mm Audio Jack [package=audio-jack]
  LED3 = LED - 5mm [color="Red (633nm)" part_number=SLIDE package="5 mm [THT]"]
  J2 = male pin header, 6 pins [form="♂ (male)"]
  R5 = Trimmer Potentiometer [maximum_resistance=10kΩ package=THT]
  R4 = Trimmer Potentiometer [maximum_resistance=10kΩ package=THT]
  part = male pin header, 6 pins [form="♂ (male)"]  # not connected

nets:
  N1: D1.cathode, IC1.IN, C1.+
  N2: D1.anode, F1.2
  GND: IC1.GND, C1.-, C2.-, J1.GND, U1.GND, R1.Pin_1, C6.0, R3.Pin_0, C3.1, R6.Pin_1, R9.Pin_1, Q1.E, U4.Pin_2, U5.Pin_2, J2.pin6, R5.leg1, R4.leg1
  N3: IC1.OUT, C2.+, LED1.anode, U1.VCC, U1.AVCC, U1.AREF, R2.Pin_1, S2.Pin_1, S2.Pin_2, D2.cathode, U2.2, R5.leg2, R4.leg2
  N4: J1.PWR, S1.COM
  N5: LED1.cathode, R1.Pin_0
  N6: U1.RESET, R2.Pin_0, C5.1
  N7: U1.D0_(RX), J2.pin3
  N8: U1.D1_(TX), J2.pin2
  N9: U1.D3_(PWM), S2.Pin_3, S2.Pin_4, R6.Pin_0
  N10: U1.XLAT1, XTAL1.pin_0, C6.1
  N11: U1.XLAT2, XTAL1.pin_1, C3.0
  N12: U1.D8, LED3.anode
  N13: U1.D9_(PWM), LED5.anode
  N14: U1.D10_(PWM), LED4.anode
  N15: U1.D13, LED2.cathode, LED2.anode, R3.Pin_1
  N16: U1.A0, R5.wiper
  N17: U1.A1, R4.wiper
  N18: C5.0, J2.pin1
  N19: F1.1, S1.L2
  N20: D2.anode, Q1.C, U2.9
  N21: R8.Pin_0, LED3.cathode
  N22: R8.Pin_1, R9.Pin_0, Q1.B
  N23: U3.RIGHT, U2.10
  N24: U3.SLEEVE, U2.6
  N25: U4.Pin_1, R10.Pin_0
  N26: U4.Pin_4, U5.Pin_4, U6.SLEEVE
  N27: U4.Pin_5, U6.LEFT
  N28: LED4.cathode, R10.Pin_1
  N29: LED5.cathode, R11.Pin_1
  N30: R11.Pin_0, U5.Pin_1
  N31: U5.Pin_5, U6.RIGHT

notes:
  RST
  Rx
  Tx
  GND
  +5V
  DELAY 1
  DELAY 2
  OPER
  STAT
  to projector remote
  to camera remote
  Vin (9-12v DC)
  programming connector
  DSLR Slide Sacnner, Arduino controller schematics, 1
