# Fritzing sketch id1502_Bench_Power_system_0 (saved by Fritzing 0.9.1b)
breadboards: 1

parts:
  VCC1 = Battery
  D1 = Rectifier Diode [part_number=1N4001 package="300 mil [THT]"]
  D3 = Rectifier Diode [part_number=1N4001 package="Melf DO-213 AB [SMD]"]
  V1 = AC Power [voltage=5 frequency=60]
  Power_plug1 = Power plug

nets:
  N1: VCC1.+, D3.anode
  N2: D1.cathode, D3.cathode
  N3: D1.anode, V1.V-
  GND: Power_plug1.GND

notes:
  DC Supply
  [Battery Outside
  DC Socket (several different types avaiable.
  [wWhen the power goes away, the battery power takes over.
