# Fritzing sketch id1503_DualAnalogToSerial_0 (saved by Fritzing 0.9.2b)
breadboards: 1

parts:
  Part1 = Arduino Uno (Rev3)
  Part2 = Thumb Joystick
  Part3 = Thumb Joystick

nets:
  N1: Part1.A0, Part2.VERT
  N2: Part1.A1, Part2.HORZ
  N3: Part1.A2, Part3.VERT
  N4: Part1.A3, Part3.HORZ
  N5: Part1.D2, Part2.SEL
  N6: Part1.D4, Part3.SEL
  VCC: Part1.5V, Part2.VCC, Part3.VCC
  GND: Part1.GND, Part2.GND, Part3.GND

notes:
  Arduino 5V -> Vcc
  Arduino GND -> GND
  Arduino A0 -> VER
  Arduino A1 -> HOR
  Arduino 2 -> SEL
  Arduino 5V -> Vcc
  Arduino GND -> GND
  Arduino A2 -> VER
  Arduino A3 -> HOR
  Arduino 4 -> SEL
