# Fritzing sketch id1504_Schematic_0 (saved by Fritzing 0.9.3b)
breadboards: 1

parts:
  U1 = LCD-16X2 [package=lcd-16x2_noholes]
  hc-sr1 = hc-sr04
  hc-sr2 = hc-sr04
  Part1 = Arduino Uno (Rev3) - ICSP
  R1 = Trimmer Potentiometer [maximum_resistance=10kΩ package=THT]
  R2 = Resistor [tolerance=±5% resistance=220 package=THT]

nets:
  GND: U1.VSS, U1.R_W, hc-sr1.GND, Part1.GND
  VDD: U1.VDD, hc-sr1.VCC, Part1.5V
  N1: U1.VO, R1.wiper
  N2: U1.RS, Part1.D12/MISO
  N3: U1.E, Part1.D11_PWM/MOSI
  N4: U1.DB4, Part1.D5_PWM
  N5: U1.DB5, Part1.D4
  N6: U1.DB6, Part1.D3_PWM
  N7: U1.DB7, Part1.D2
  N8: U1.A, hc-sr2.VCC, R1.leg2, R2.Pin_0, R2.Pin_1
  N9: U1.K, hc-sr2.GND, R1.leg1
  N10: hc-sr1.Trig, Part1.D9_PWM
  N11: hc-sr1.Echo, Part1.D8
  N12: hc-sr2.Trig, Part1.D7
  N13: hc-sr2.Echo, Part1.D6_PWM
