# Fritzing sketch id1505_Dual_stepper_0 (saved by Fritzing 0.7.7b)
breadboards: 1

parts:
  Arduino1 = Arduino
  MD09B1 = A4988_Stepper_Motor_Driver_Carrier
  MD09B2 = A4988_Stepper_Motor_Driver_Carrier
  J1 = Screw terminal - 2 pins [package=THT]
  J2 = Screw terminal - 2 pins [package=THT]
  J3 = Screw terminal - 2 pins [package=THT]
  J4 = Screw terminal - 2 pins [package=THT]
  J5 = Screw terminal - 2 pins [package=THT]

nets:
  N1: Arduino1.D12, MD09B1.connector130
  N2: Arduino1.D11, MD09B2.connector130
  N3: Arduino1.D10, MD09B1.connector131, MD09B2.connector131
  N4: Arduino1.D9, MD09B1.connector132, MD09B2.connector132
  N5: Arduino1.D8, MD09B1.connector133, MD09B2.connector133
  N6: Arduino1.D7, MD09B1.connector135, MD09B2.connector135
  N7: Arduino1.D6, MD09B1.connector136, MD09B2.connector136
  N8: Arduino1.D5, MD09B1.connector137, MD09B2.connector137
  N9: Arduino1.RST, MD09B1.connector134, MD09B2.connector134
  N10: Arduino1.+5V, MD09B1.connector146, MD09B2.connector146
  N11: Arduino1.GND, MD09B1.connector147, MD09B2.connector147
  N12: MD09B1.connector140, MD09B2.connector140, J3.pin1
  N13: MD09B1.connector141, MD09B2.connector141, J3.pin2
  N14: MD09B1.connector142, J1.pin2
  N15: MD09B1.connector143, J1.pin1
  N16: MD09B1.connector144, J2.pin2
  N17: MD09B1.connector145, J2.pin1
  N18: MD09B2.connector142, J4.pin1
  N19: MD09B2.connector143, J4.pin2
  N20: MD09B2.connector144, J5.pin1
  N21: MD09B2.connector145, J5.pin2
