# Fritzing sketch id1506_DUAL_VOLTAGE_REG_V1_0 (saved by Fritzing 0.9.0b)
circuit board: 8.46667cm x 5.64444cm
breadboards: 1

parts:
  U1 = NTE966
  U2 = NTE964
  J1 = Screw terminal - 2 pins [package=THT]
  J2 = Screw terminal - 2 pins [package=THT]
  J3 = Screw terminal - 2 pins [package=THT]
  C1 = Electrolytic Capacitor [capacitance=2.2mF voltage=35V package="300 mil [THT, electrolytic]"]
  C2 = Electrolytic Capacitor [capacitance=1mF voltage=20V package="200 mil [THT, electrolytic]"]
  C3 = Electrolytic Capacitor [capacitance=3.3mF voltage=16V package="200 mil [THT, electrolytic]"]
  LED1 = LED - 5mm [color="Green (565nm)" package="5 mm [THT]"]
  LED2 = LED - 5mm [color="Blue (505nm)" package="5 mm [THT]"]
  R1 = Resistor [tolerance=±5% resistance=330 package=THT]
  R2 = Resistor [tolerance=±5% resistance=330 package=THT]

nets:
  N1: U1.connector0, U1.connector2, U2.connector0, U2.connector2, J1.pin2, J2.pin2, J3.pin2, C1.+, C2.+, C3.+, LED1.cathode, LED2.cathode
  N2: U1.connector1, U2.connector1, J1.pin1, J2.pin1, J3.pin1, C1.-, C2.-, C3.-, R1.Pin_1, R2.Pin_1
  N3: LED1.anode, R1.Pin_0
  N4: LED2.anode, R2.Pin_0
