# Fritzing sketch id1508_Due_led_88tIlJZ_0 (saved by Fritzing 0.9.3b)
circuit board: 8.46667cm x 5.64444cm
breadboards: 1

parts:
  Componente1 = Arduino Uno (Rev3)
  R1 = Resistor [tolerance=±5% resistance=220 package=THT]
  R2 = Resistor [tolerance=±5% resistance=220 package=THT]
  LED1 = LED - 5mm [color="Red (633nm)" package="5 mm [THT]"]
  LED2 = LED - 5mm [color="Green (560nm)" package="5 mm [THT]"]

nets:
  N1: Componente1.D9_PWM, LED1.anode, LED2.cathode
  N2: Componente1.GND, R2.Pin_0
  N3: Componente1.5V, R1.Pin_1
  N4: R1.Pin_0, LED2.anode
  N5: R2.Pin_1, LED1.cathode
