# Fritzing sketch id1510_Duo_LED_0 (saved by Fritzing 0.9.3b)
breadboards: 1

parts:
  Part1 = Arduino Uno (Rev3)
  LED1 = prefix0000
  LED2 = prefix0000
  LED3 = prefix0000

nets:
  N1: Part1.D8, LED1.connector4
  N2: Part1.D9_PWM, LED1.connector0
  N3: Part1.D2, LED3.connector4
  N4: Part1.D3_PWM, LED3.connector0
  N5: Part1.D5_PWM, LED2.connector4
  N6: Part1.D6_PWM, LED2.connector0
  N7: Part1.GND, LED1.connector1, LED2.connector1, LED3.connector1

notes:
  Meg van a három (Piros/Kék) közös katódos Duó LED.
  Hogyha közös anódos, akkor kigyullad a LED.
  Az első LEDet dugjuk be, a másikat fordítva, azutolsót pedig ugyanúgy mint az elsőt.
  It has three (Red/Blue) common cathode LED Duo.
  If a common anode, then the LED will light up.
  The first pin when LED light, and the other way round and the last one the same way as the first.
  Jó munkát kívánok!
  May you have a nice day at work!
