# Fritzing sketch id1511_FritZing_0 (saved by Fritzing 0.9.3b)
breadboards: 1

parts:
  Part1 = Arduino Uno (Rev3)
  LED8 = DUO LED RG [color="Red (633nm)" package="5 mm [THT]"]

nets:
  N1: Part1.GND, LED8.common_cathode
  N2: Part1.D4, LED8.green_anode
  N3: Part1.D7, LED8.red_anode

notes:
  Duó LED Egyszerűen
