# Fritzing sketch id1512_Durchschalter_0 (saved by Fritzing 0.8.5b)
breadboards: 1

parts:
  Q2 = Basic FET N-Channel [package="TO220 [THT]"]
  Q3 = Basic FET N-Channel [package="TO220 [THT]"]
  R1 = Resistor [tolerance=±5% resistance=4.7k package=THT]
  R2 = Resistor [tolerance=±5% resistance=470 package=THT]
  Power_plug1 = Power plug [part_number=9V]
  LED1 = LED - 5mm [color="Red (633nm)" package="5 mm [THT]"]
  C1 = Ceramic Capacitor [capacitance=100nF package="100 mil [THT, multilayer]"]
  C2 = Ceramic Capacitor [capacitance=100nF package="100 mil [THT, multilayer]"]
  R3 = Resistor [tolerance=±5% resistance=10k package=THT]
  R4 = Resistor [tolerance=±5% resistance=10k package=THT]
  R5 = Resistor [tolerance=±5% resistance=10k package=THT]
  LED2 = LED - 5mm [color="Red (633nm)" package="5 mm [THT]"]
  LED3 = LED - 5mm [color="Red (633nm)" package="5 mm [THT]"]
  R6 = Resistor [tolerance=±5% resistance=470 package=THT]
  R7 = Resistor [tolerance=±5% resistance=220 package=THT]
  R8 = Resistor [tolerance=±5% resistance=220 package=THT]
  S1 = Pushbutton [package="[THT]"]
  R9 = Resistor [tolerance=±5% resistance=47k package=THT]
  R10 = Resistor [tolerance=±5% resistance=47k package=THT]
  C3 = Electrolytic Capacitor [capacitance=47µF package="100 mil [THT, electrolytic]"]
  Q9 = PNP-Transistor [package="TO92 [THT]"]
  Q6 = PNP-Transistor [package="TO92 [THT]"]
  Q11 = NPN-Transistor [package="TO92 [THT]"]
  Q4 = NPN-Transistor [package="TO92 [THT]"]
  Q8 = PNP-Transistor [package="TO92 [THT]"]
  Q10 = NPN-Transistor [package="TO92 [THT]"]
  Q7 = PNP-Transistor [package="TO92 [THT]"]
  Q5 = PNP-Transistor [package="TO92 [THT]"]
  Q12 = PNP-Transistor [package="TO92 [THT]"]
  Bauteil1 = Variable Capacitor [capacitance=100nF max_capacitance=10pF min_capacitance=2pF voltage=35V]
  Q13 = PNP-Transistor [package="TO92 [THT]"]
  R11 = Resistor [tolerance=±5% resistance=220 package=THT]
  R12 = Resistor [tolerance=±5% resistance=220 package=THT]
  Q14 = NPN-Transistor [package="TO92 [THT]"]
  Q15 = NPN-Transistor [package="TO92 [THT]"]
  Q16 = NPN-Transistor [package="TO92 [THT]"]
  C4 = Electrolytic Capacitor [capacitance=1µF package="100 mil [THT, electrolytic]"]
  C5 = Electrolytic Capacitor [capacitance=1µF package="100 mil [THT, electrolytic]"]
  S2 = Pushbutton [package="[THT]"]
  R13 = Resistor [tolerance=±5% resistance=220 package=THT]
  Q17 = NPN-Transistor [package="TO92 [THT]"]
  Q18 = NPN-Transistor [package="TO92 [THT]"]
  Q19 = NPN-Transistor [package="TO92 [THT]"]
  Q20 = NPN-Transistor [package="TO92 [THT]"]
  Q21 = NPN-Transistor [package="TO92 [THT]"]
  Q22 = NPN-Transistor [package="TO92 [THT]"]  # not connected
  Q23 = NPN-Transistor [package="TO92 [THT]"]
  Q24 = MOSFET-NCHANNEL [package=to-92]
  Q25 = MOSFET-NCHANNEL [package=to-92]
  Q26 = MOSFET-NCHANNEL [package=to-92]
  Q27 = MOSFET-NCHANNEL [package=to-92]
  Q28 = MOSFET-NCHANNEL [package=to-92]
  Q29 = MOSFET-NCHANNEL [package=to-92]
  C6 = Ceramic Capacitor [capacitance=100nF package="100 mil [THT, multilayer]"]
  C7 = Ceramic Capacitor [capacitance=100nF package="100 mil [THT, multilayer]"]
  C8 = Ceramic Capacitor [capacitance=100nF package="100 mil [THT, multilayer]"]
  C9 = Ceramic Capacitor [capacitance=100nF package="100 mil [THT, multilayer]"]
  C10 = Ceramic Capacitor [capacitance=100nF package="100 mil [THT, multilayer]"]
  C11 = Ceramic Capacitor [capacitance=100nF package="100 mil [THT, multilayer]"]
  R14 = Resistor [tolerance=±5% resistance=1k package=THT]
  R15 = Resistor [tolerance=±5% resistance=1k package=THT]
  R16 = Resistor [tolerance=±5% resistance=1k package=THT]
  Q30 = NPN-Transistor [package="TO92 [THT]"]
  Q31 = NPN-Transistor [package="TO92 [THT]"]

nets:
  N1: Q2.gate, C1.1, Q8.C, Q16.C
  GND: Q2.drain, Q3.drain, Q10.C, Q30.C, Q31.C
  N2: Q2.source, R2.Pin_0, C1.0, R3.Pin_0, Q11.C, C4.+, C5.-, S2.Pin_3, S2.Pin_4
  N3: Q3.gate, C2.1, Q9.C, Q15.C
  N4: Q3.source, C2.0, R4.Pin_0
  N5: R1.Pin_0, Q4.B
  N6: R1.Pin_1, Power_plug1.GND, S1.Pin_1, S1.Pin_2, C3.+, Q9.E, Q6.E, Q8.E, Q7.E, Q5.E, Q12.E
  N7: LED1.anode, Q5.C
  N8: R3.Pin_1, Q6.B, Q12.C
  N9: R4.Pin_1, Q7.B
  N10: R5.Pin_0, Q4.E
  N11: R5.Pin_1, Q5.B
  N12: LED2.anode, Q6.C, R12.Pin_1
  N13: LED3.anode, Q7.C, R11.Pin_1
  N14: R6.Pin_0, Q12.B
  N15: R7.Pin_0, Q10.E
  N16: R7.Pin_1, Q8.B
  N17: R8.Pin_0, Q11.E
  N18: R8.Pin_1, Q9.B
  N19: S1.Pin_3, S1.Pin_4, R9.Pin_0, R10.Pin_0
  N20: R9.Pin_1, Q10.B
  N21: R10.Pin_1, Q11.B, Bauteil1.0
  N22: Q13.B, R12.Pin_0
  N23: Q13.C, Q16.E
  N24: R11.Pin_0, Q14.B
  N25: Q14.C, Q15.E
  N26: Q15.B, Q16.B, R13.Pin_1
  N27: S2.Pin_2, R13.Pin_0
  N28: Q17.E, Q24.D
  N29: Q17.B, Q20.B, R14.Pin_1
  N30: Q18.E, Q25.D
  N31: Q18.B, Q21.B, R15.Pin_1
  N32: Q19.E, Q26.D
  N33: Q19.B, Q23.B, R16.Pin_1
  N34: Q19.C, Q30.E
  N35: Q20.E, Q27.D
  N36: Q21.E, Q28.D
  N37: Q23.E, Q29.D
  N38: Q23.C, Q31.E
  N39: Q24.S, C8.0
  N40: Q24.G, C8.1
  N41: Q25.S, C6.0
  N42: Q25.G, C6.1
  N43: Q26.S, C7.0
  N44: Q26.G, C7.1
  N45: Q27.S, C11.0
  N46: Q27.G, C11.1
  N47: Q28.S, C10.0
  N48: Q28.G, C10.1
  N49: Q29.S, C9.0
  N50: Q29.G, C9.1

notes:
  Taster oder Eingangssignal, um vor zu schalten.
  nächster Transistor sperrt wenn er an ist diesen schalter/Transistor.
