# Fritzing sketch id1513_DustSensorToPiezo_0 (saved by Fritzing 0.9.0b)
breadboards: 1

parts:
  Part1 = Arduino Uno (Rev3)
  C1 = Electrolytic Capacitor [capacitance=1µF package="100 mil [THT, electrolytic]"]
  R1 = Resistor [tolerance=±5% resistance=220 package=THT]
  J1 = Piezo Speaker

nets:
  N1: Part1.D8, J1.pin2
  N2: Part1.GND, C1.-, J1.pin1
  N3: Part1.5V, R1.Pin_0
  N4: C1.+, R1.Pin_1

notes:
  Optical Dust Sensor
  1 2 3 4 5 6
  1  2  3  4  5  6
