# Fritzing sketch id1515_Digital_Thermometer___Thermistor_10k_ (saved by Fritzing 0.6.5b)
breadboards: 2

parts:
  LCD_Nokia_1 = LCD_Nokia_5110 [part_number="Nokia 5110"]
  R5 = Temperature Sensor (Thermistor) [thermistor_type=NTC package=THT]
  R6 = Resistor [tolerance=±5% resistance=10k package=THT]
  S1 = Pushbutton [package="[THT]"]
  S2 = Pushbutton [package="[THT]"]
  R7 = Resistor [tolerance=±5% resistance=2.2k package=THT]
  R8 = Resistor [tolerance=±5% resistance=2.2k package=THT]
  10kΩ = Resistor [tolerance=±5% resistance=10k package=THT]
  R10 = Resistor [tolerance=±5% resistance=10k package=THT]
  CR2032_Cell_holder_3v1 = C2032_Cell_Holder_3v
  SD_Card_YwRobot1 = SD_Card_YwRobot
  XTAL1 = Crystal [frequency="16 Mhz" package=THT]
  IC2 = DS1307 [package=THT]
  C1 = Ceramic Capacitor [capacitance=100nF package="100 mil [THT, multilayer]"]
  U1 = atmega168 [package="DIP28 [THT]"]
  XTAL2 = Crystal [frequency="16 Mhz" package=THT]
  C2 = Ceramic Capacitor [capacitance=22pF package="100 mil [THT, multilayer]"]
  U3 = Voltage Regulator - 5V [package="TO220 [THT]"]
  C3 = Ceramic Capacitor [capacitance=22pF package="100 mil [THT, multilayer]"]
  U2 = Voltage Regulator - 3.3V [package="TO220 [THT]"]
  C4 = Ceramic Capacitor [capacitance=0.33µF package="100 mil [THT, multilayer]"]
  C5 = Ceramic Capacitor [capacitance=0.1µF package="100 mil [THT, multilayer]"]
  VCC1 = Battery block 9V
  C6 = Ceramic Capacitor [capacitance=100nF package="100 mil [THT, multilayer]"]
  C7 = Electrolytic Capacitor [capacitance=10µF package="100 mil [THT, electrolytic]"]

nets:
  N1: LCD_Nokia_1.connector9, U1.Pin_5
  N2: LCD_Nokia_1.connector10, U1.Pin_6
  N3: LCD_Nokia_1.connector11, U1.Pin_11
  N4: LCD_Nokia_1.connector12, U1.Pin_12
  N5: LCD_Nokia_1.connector13, U1.Pin_13
  N6: LCD_Nokia_1.connector14, U1.Pin_8, U1.Pin_22, C2.1, U3.GND, C3.0, C4.0, C5.1, VCC1.-
  N7: LCD_Nokia_1.connector15, R5.pin_1, S1.Pin_3, S1.Pin_4, S2.Pin_3, S2.Pin_4, SD_Card_YwRobot1.connector0, SD_Card_YwRobot1.connector2, IC2.+V, C1.1, U1.Pin_7, U1.Pin_20, U3.output_voltage, U2.input_voltage, C5.0, C7.-
  N8: R5.pin_0, R6.Pin_1, U1.Pin_23
  N9: R6.Pin_0, 10kΩ.Pin_1, R10.Pin_1, CR2032_Cell_holder_3v1.connector1, SD_Card_YwRobot1.connector1, SD_Card_YwRobot1.connector3, IC2.0V, C1.0, U2.GND, C6.1, C7.+
  N10: S1.Pin_1, S1.Pin_2, 10kΩ.Pin_0, U1.Pin_14
  N11: S2.Pin_1, S2.Pin_2, R10.Pin_0, U1.Pin_4
  N12: R7.Pin_0, IC2.SDA_-_I2C_Data, U1.Pin_27
  N13: R8.Pin_0, IC2.SCL_-_I2C_Clock, U1.Pin_28
  N14: CR2032_Cell_holder_3v1.connector0, IC2.Vbat_-_Backup_Supply
  N15: SD_Card_YwRobot1.connector4, U1.Pin_16
  N16: SD_Card_YwRobot1.connector5, U1.Pin_17
  N17: SD_Card_YwRobot1.connector6, U1.Pin_19
  N18: SD_Card_YwRobot1.connector7, U1.Pin_18
  N19: SD_Card_YwRobot1.connector8, U1.Pin_15
  N20: XTAL1.pin_0, IC2.X2_-_Crystal
  N21: XTAL1.pin_1, IC2.X1_-_Crystal
  N22: U1.Pin_9, XTAL2.pin_0, C3.1
  N23: U1.Pin_10, XTAL2.pin_1, C2.0
  N24: U3.input_voltage, U2.output_voltage, C4.1, VCC1.+, C6.0

notes:
  LCD Nokia 5110
  32.768 kHz
  CR2032 Cell Holder Li Battery 3V
  SD Card
  7805CV
  LD33CV
