# Fritzing sketch id1515_dX2_0 (saved by Fritzing 0.7.5b)

parts:
  J1 = female pin header, 2 pins [form="♀ (female)"]
  J2 = female pin header, 4 pins [form="♀ (female)"]
  U1 = attiny85 [package=dip]
  J3 = female pin header, 4 pins [form="♀ (female)"]
  D1 = Schottky Diode [part_number=1N5817 package="300 mil [THT]"]
  C1 = Electrolytic Capacitor [capacitance=10µF package="100 mil [THT, electrolytic]"]
  C2 = Electrolytic Capacitor [capacitance=10µF package="100 mil [THT, electrolytic]"]
  MENU = Pushbutton [package="[THT]"]
  RL/- = Pushbutton [package="[THT]"]
  SL/+ = Pushbutton [package="[THT]"]

nets:
  N1: J1.pin1, D1.anode
  N2: J1.pin2, J2.pin3, U1.Pin_4, J3.pin2, C1.-, C2.-, MENU.Pin_1, MENU.Pin_2, RL/-.Pin_1, RL/-.Pin_2, SL/+.Pin_1, SL/+.Pin_2
  N3: J2.pin1, J2.pin4, J3.pin1, D1.cathode, C1.+
  N4: J2.pin2, U1.Pin_8, C2.+
  N5: U1.Pin_2, RL/-.Pin_3, RL/-.Pin_4
  N6: U1.Pin_3, SL/+.Pin_3, SL/+.Pin_4
  N7: U1.Pin_5, J3.pin3
  N8: U1.Pin_6, MENU.Pin_3, MENU.Pin_4
  N9: U1.Pin_7, J3.pin4

notes:
  +
  Vin
  Gnd
  VCC
  SCL
  D
  10uF
  kreativekorp.com/dX/oed/
  dX
  Overengineered
  Electronic Die
  SDA
  Vout
  GND
