# Fritzing sketch id1516_Esqyema_Frizing_0 (saved by Fritzing 0.9.3b)

parts:
  Arduino_Nano_+_Shield = arduino_nano_v3.0_io_expansion
  Modulo_bluetooth = Bluetooth HC-06
  hc-sr1_(ultrasonido) = HC-SR04
  Zumbador = KY-006
  Matriz_LEDs_8x8 = LED_matrix_8x8
  Servo_brazo_drch = servo360
  Servo_brazo_izq = servo360
  Servo_rueda_drch = servo360
  Servo_rueda = servo360
  Seguidor_linia = TCRT5000_Line_Tracker

nets:
  N1: Arduino_Nano_+_Shield.connector20, Modulo_bluetooth.connector2
  N2: Arduino_Nano_+_Shield.connector21, Servo_rueda_drch.connector1
  N3: Arduino_Nano_+_Shield.connector22, Modulo_bluetooth.connector3
  N4: Arduino_Nano_+_Shield.connector23, Servo_brazo_drch.connector1
  N5: Arduino_Nano_+_Shield.connector24, Servo_rueda.connector1
  N6: Arduino_Nano_+_Shield.connector25, hc-sr1_(ultrasonido).connector3
  N7: Arduino_Nano_+_Shield.connector26, Zumbador.connector0
  N8: Arduino_Nano_+_Shield.connector27, Servo_brazo_izq.connector1
  N9: Arduino_Nano_+_Shield.connector28, Matriz_LEDs_8x8.connector3
  N10: Arduino_Nano_+_Shield.connector29, Matriz_LEDs_8x8.connector5
  N11: Arduino_Nano_+_Shield.connector30, Matriz_LEDs_8x8.connector2
  N12: Arduino_Nano_+_Shield.connector42, Seguidor_linia.connector3
  N13: Arduino_Nano_+_Shield.connector45, hc-sr1_(ultrasonido).connector2
  N14: Arduino_Nano_+_Shield.connector52, Modulo_bluetooth.connector1
  N15: Arduino_Nano_+_Shield.connector53, Servo_rueda_drch.connector3
  N16: Arduino_Nano_+_Shield.connector55, Servo_brazo_drch.connector3
  N17: Arduino_Nano_+_Shield.connector56, Servo_rueda.connector3
  N18: Arduino_Nano_+_Shield.connector58, Zumbador.connector2
  N19: Arduino_Nano_+_Shield.connector59, Servo_brazo_izq.connector3
  N20: Arduino_Nano_+_Shield.connector62, Matriz_LEDs_8x8.connector1
  N21: Arduino_Nano_+_Shield.connector63, hc-sr1_(ultrasonido).connector4
  N22: Arduino_Nano_+_Shield.connector68, Seguidor_linia.connector1
  N23: Arduino_Nano_+_Shield.connector81, Modulo_bluetooth.connector0
  N24: Arduino_Nano_+_Shield.connector82, Servo_rueda_drch.connector2
  N25: Arduino_Nano_+_Shield.connector84, Servo_brazo_drch.connector2
  N26: Arduino_Nano_+_Shield.connector85, Servo_rueda.connector2
  N27: Arduino_Nano_+_Shield.connector87, Zumbador.connector3
  N28: Arduino_Nano_+_Shield.connector88, Servo_brazo_izq.connector2
  N29: Arduino_Nano_+_Shield.connector91, Matriz_LEDs_8x8.connector0
  N30: Arduino_Nano_+_Shield.connector92, hc-sr1_(ultrasonido).connector1
  N31: Arduino_Nano_+_Shield.connector97, Seguidor_linia.connector0

notes:
  VISTA FRONTAL
  VISTA INFERIOR
