# Fritzing sketch id1517_DIL_16_Shield (saved by Fritzing 0.6.3b)
breadboards: 1

parts:
  Arduino1 = Arduino
  J1 = female pin header, 8 pins [form="♀ (female)"]
  J2 = female pin header, 8 pins [form="♀ (female)"]
  R1 = Resistor [tolerance=±5% resistance=1k package=THT]
  Power = LED - 5mm [color="Red (633nm)" package="5 mm [THT]"]
  R2 = Resistor [tolerance=±5% resistance=470 package=THT]
  Reset = Pushbutton [package="[THT]"]
  DIP-16 = mystery part, 16 pins [chip_label=DIL-16 spacing=300mil]

nets:
  N1: Arduino1.GND, Power.cathode, Reset.Pin_3, Reset.Pin_4
  N2: Arduino1.RST, R1.Pin_1, Reset.Pin_1, Reset.Pin_2
  N3: Arduino1.+5V, R1.Pin_0, R2.Pin_0
  N4: J1.pin1, DIP-16.pin1
  N5: J1.pin2, DIP-16.pin2
  N6: J1.pin3, DIP-16.pin3
  N7: J1.pin4, DIP-16.pin4
  N8: J1.pin5, DIP-16.pin5
  N9: J1.pin6, DIP-16.pin6
  N10: J1.pin7, DIP-16.pin7
  N11: J1.pin8, DIP-16.pin8
  N12: J2.pin1, DIP-16.pin16
  N13: J2.pin2, DIP-16.pin15
  N14: J2.pin3, DIP-16.pin14
  N15: J2.pin4, DIP-16.pin13
  N16: J2.pin5, DIP-16.pin12
  N17: J2.pin6, DIP-16.pin11
  N18: J2.pin7, DIP-16.pin10
  N19: J2.pin8, DIP-16.pin9
  N20: Power.anode, R2.Pin_1

notes:
  1
  16
  9
  8
  470Ω
  1kΩ
  DIL-16 Shield
  by Felix Morgner
  felixmorgner.ch
