# Fritzing sketch id1518_dyor_0 (saved by Fritzing 0.9.3b)

parts:
  U1 = TCRT5000_Line_Tracker
  ZUMBADOR = KY-006
  hc-sr1 = HC-SR04
  BLUETOOTH = Bluetooth HC-06
  R1 = servo360 [part_number=MI1]
  R3 = servo360 [part_number=SD1]
  R4 = servo360 [part_number=SI1]
  R2 = servo360 [part_number=MD1]
  ARDUINO01 = arduino_nano_v3.0_io_expansion
  U2 = LED_matrix_8x8

nets (from the breadboard view):
  N1: U1.connector0, ARDUINO01.connector104
  N2: U1.connector1, ARDUINO01.connector68
  N3: U1.connector3, ARDUINO01.connector42
  N4: ZUMBADOR.connector0, ARDUINO01.connector26
  N5: ZUMBADOR.connector2, ARDUINO01.connector58
  N6: ZUMBADOR.connector3, ARDUINO01.connector87
  N7: hc-sr1.connector1, ARDUINO01.connector92
  N8: hc-sr1.connector2, ARDUINO01.connector45
  N9: hc-sr1.connector3, ARDUINO01.connector25
  N10: hc-sr1.connector4, ARDUINO01.connector63
  N11: BLUETOOTH.connector0, ARDUINO01.connector81
  N12: BLUETOOTH.connector1, ARDUINO01.connector52
  N13: BLUETOOTH.connector2, ARDUINO01.connector20
  N14: BLUETOOTH.connector3, ARDUINO01.connector22
  N15: R1.connector1, ARDUINO01.connector27
  N16: R1.connector2, ARDUINO01.connector88
  N17: R1.connector3, ARDUINO01.connector59
  N18: R3.connector1, ARDUINO01.connector21
  N19: R3.connector2, ARDUINO01.connector82
  N20: R3.connector3, ARDUINO01.connector53
  N21: R4.connector1, ARDUINO01.connector24
  N22: R4.connector2, ARDUINO01.connector85
  N23: R4.connector3, ARDUINO01.connector56
  N24: R2.connector1, ARDUINO01.connector23
  N25: R2.connector2, ARDUINO01.connector84
  N26: R2.connector3, ARDUINO01.connector55
  N27: ARDUINO01.connector28, U2.connector3
  N28: ARDUINO01.connector30, U2.connector2
  N29: ARDUINO01.connector62, U2.connector1
  N30: ARDUINO01.connector91, U2.connector0
