# Fritzing sketch id1519_easy_atmel328_0 (saved by Fritzing 0.8.6b)
circuit board: 2.61744cm x 5.6817cm
breadboards: 1

parts:
  U1 = atmega328 [package=dip]
  J1 = female pin header, 2 pins [form="♀ (female)"]
  Power_plug1 = Power plug
  U2 = Voltage Regulator - 5V [package="TO220 [THT]"]
  Y1 = Resonator [frequency="16 Mhz" package=THT]
  J2 = double row female pin header, 6 pins [form="♀ (female)"]
  J3 = female pin header, 2 pins [form="♀ (female)"]
  J4 = female pin header, 5 pins [form="♀ (female)"]
  J5 = female pin header, 4 pins [form="♀ (female)"]
  J6 = female pin header, 6 pins [form="♀ (female)"]
  J7 = female pin header, 5 pins [form="♀ (female)"]
  J8 = female pin header, 2 pins [form="♀ (female)"]
  LED1 = smd LED [color="Red (633nm)" package="0603 [SMD]"]
  R1 = Resistor [tolerance=±5% resistance=220 package="0603 [SMD]"]
  C1 = Ceramic Capacitor [capacitance=1nF package="0603 [SMD, multilayer]"]

nets:
  N1: U1.RESET, J2.pin3
  N2: U1.D0_(RX), J3.pin1, J4.pin1
  N3: U1.D1_(TX), J3.pin2, J4.pin2
  N4: U1.D2, J4.pin3
  N5: U1.D3_(PWM), J4.pin4
  N6: U1.D4, J4.pin5
  N7: U1.VCC, U1.AVCC, J1.pin2, U2.output_voltage, J2.pin6
  GND: U1.GND, J1.pin1, Power_plug1.GND, U2.GND, Y1.GND, J2.pin4, J8.pin2, LED1.anode, C1.1
  N8: U1.XLAT1, Y1.0
  N9: U1.XLAT2, Y1.pin_1
  N10: U1.D5_(PWM), J5.pin1
  N11: U1.D6_(PWM), J5.pin2
  N12: U1.D7, J5.pin3
  N13: U1.D8, J5.pin4
  N14: U1.D9_(PWM), J7.pin5
  N15: U1.D10_(PWM), J7.pin4
  N16: U1.D11_(PWM), J2.pin5, J7.pin3
  N17: U1.D12, J2.pin1, J7.pin2
  N18: U1.D13, J2.pin2, J7.pin1, R1.Pin_1
  N19: U1.AREF, C1.0
  N20: U1.A0, J6.pin6
  N21: U1.A1, J6.pin5
  N22: U1.A2, J6.pin4
  N23: U1.A3, J6.pin3
  N24: U1.A4, J6.pin2
  N25: U1.A5, J6.pin1
  N26: Power_plug1.VCC, U2.input_voltage, J8.pin1
  N27: LED1.cathode, R1.Pin_0

notes:
  RX
  TX
  D
  A
  0
  1
  2
  3
  4
  +
  -
  5
  6
  7
  8
  13
  12
  11
  10
  9
  9V DC
  5V DC
  Tomcore Electronics
  Easy Atmel 328
