# Fritzing sketch id151_555_monostable_0 (saved by Fritzing 0.9.0b)
breadboards: 1

parts:
  U1 = 555 Timer [package="DIP8 [THT]"]
  R1 = Resistor [tolerance=±5% resistance=10k package=THT]
  S1 = Pushbutton [package="[THT]"]
  C1 = Electrolytic Capacitor [capacitance=47µF voltage=35V package="200 mil [THT, electrolytic]"]
  R2 = Rotary Potentiometer (Large) [maximum_resistance=100kΩ package=THT]
  LED1 = LED - 5mm [color="Red (633nm)" package="5 mm [THT]"]
  R3 = Resistor [tolerance=±5% resistance=220 package=THT]

nets:
  GND: U1.Ground, S1.Pin_3, S1.Pin_4, C1.-, R3.Pin_1
  N1: U1.Trigger, R1.Pin_0, S1.Pin_1, S1.Pin_2
  N2: U1.Output, LED1.anode
  5V: U1.Reset, U1.Vcc_Supply_Voltage, R1.Pin_1, R2.wiper
  N3: U1.Threshold, U1.Discharge, C1.+, R2.leg2
  N4: LED1.cathode, R3.Pin_0

notes:
  recuerden que a veces las líneas se cruzan en el dibujo pero sólo las que tienen el punto negro están conectadas entre sí.
