# Fritzing sketch id1520_Car_Design_0 (saved by Fritzing 0.9.2b)
breadboards: 1

parts:
  VCC2 = Battery
  S1 = Toggle Switch [package=THT]
  M1 = DC Motor
  M2 = DC Motor
  M3 = DC Motor
  M4 = DC Motor

nets:
  N1: VCC2.-, M1.pin_2, M2.pin_2, M3.pin_2, M4.pin_2
  N2: VCC2.+, S1.L2
  N3: S1.COM, M1.pin_1, M2.pin_1, M3.pin_1, M4.pin_1
