# Fritzing sketch id1521_clap_switch_with_monostable_and_toggle_0 (saved by Fritzing 0.7.0b)
breadboards: 3

parts:
  U1 = 555 Timer [package="DIP8 [THT]"]
  R2 = Resistor [tolerance=±5% resistance=4.7k package=THT]
  R3 = Resistor [tolerance=±5% resistance=330 package=THT]
  C1 = Electrolytic Capacitor [capacitance=100µF package="200 mil [THT, electrolytic]"]
  C2 = Ceramic Capacitor [capacitance=100nF package="200 mil [THT, multilayer]"]
  VCC1 = Battery block 9V
  Q3 = NPN-Transistor [package="TO92 [THT]"]
  Q4 = NPN-Transistor [package="TO92 [THT]"]
  R6 = Resistor [tolerance=±5% resistance=4.7k package=THT]
  R7 = Resistor [tolerance=±5% resistance=330 package=THT]
  R8 = Resistor [tolerance=±5% resistance=1k package=THT]
  R9 = Resistor [tolerance=±5% resistance=470 package=THT]
  LED2 = LED - 5mm [color="Blue (470nm)" package="5 mm [THT]"]
  C3 = Ceramic Capacitor [capacitance=100nF package="100 mil [THT, multilayer]"]
  MIC1 = Microphone
  K2 = Relay [part_number=FRS1B-S package=THT]
  U2 = 555 Timer [package="DIP8 [THT]"]
  R10 = Resistor [tolerance=±5% resistance=10k package=THT]
  R11 = Resistor [tolerance=±5% resistance=330 package=THT]
  LED3 = LED - 5mm [color="Blue (430nm)" package="5 mm [THT]"]
  R12 = Resistor [tolerance=±5% resistance=10k package=THT]
  R13 = Resistor [tolerance=±5% resistance=100k package=THT]
  D2 = Rectifier Diode [part_number=1N4001 package="300 mil [THT]"]
  BC548 = NPN-Transistor [package="TO92 [THT]"]
  R14 = Resistor [tolerance=±5% resistance=1k package=THT]
  C4 = Electrolytic Capacitor [capacitance=1µF package="100 mil [THT, electrolytic]"]

nets:
  N1: U1.Ground, C1.-, C2.1, VCC1.-, Q3.C, Q4.C, R6.Pin_0, U2.Ground, R10.Pin_1, LED3.cathode, BC548.C, C4.-
  N2: U1.Trigger, C3.1
  N3: U1.Output, R3.Pin_0
  N4: U1.Reset, U1.Vcc_Supply_Voltage, R2.Pin_0, VCC1.+, R7.Pin_0, R8.Pin_0, R9.Pin_0, K2.COIL2, U2.Reset, U2.Vcc_Supply_Voltage, R12.Pin_0, D2.cathode
  N5: U1.Control_Voltage, C2.0
  N6: U1.Threshold, U1.Discharge, R2.Pin_1, C1.+
  N7: R3.Pin_1, R14.Pin_0
  N8: Q3.E, Q4.B, R8.Pin_1
  N9: Q3.B, R6.Pin_1, MIC1.pin1
  N10: Q4.E, LED2.cathode, C3.0
  N11: R7.Pin_1, MIC1.pin2
  N12: R9.Pin_1, LED2.anode
  N13: K2.COIL1, D2.anode, BC548.E
  N14: K2.C1, K2.C2, U2.Trigger, U2.Threshold, R10.Pin_0, R12.Pin_1
  N15: K2.B, R13.Pin_0, C4.+
  N16: U2.Output, R11.Pin_0, R13.Pin_1
  N17: R11.Pin_1, LED3.anode
  N18: BC548.B, R14.Pin_1

notes:
  MIC
  This also works as a dark sensor
  This is monostable mode 555 timer module
  this is a toggle switch
  Make these three modules separately and combine them to make a clap switch
