# Fritzing sketch id1522_line_following_robot_with_ardumoto_IR_sensor_0 (saved by Fritzing 0.7.4b)
breadboards: 1

parts:
  Part1 = Arduino Motor Shield
  M1 = DC Motor
  M2 = DC Motor
  LED8 = LED - 5mm [color="Blue (430nm)" package="5 mm [THT]"]
  LED9 = LED - 5mm [color="Blue (430nm)" package="5 mm [THT]"]
  LED10 = LED - 5mm [color="Blue (430nm)" package="5 mm [THT]"]
  LED11 = LED - 3mm [color="Infrared (880nm)" package="3 mm [THT]"]
  LED12 = LED - 3mm [color="Infrared (880nm)" package="3 mm [THT]"]
  LED13 = LED - 3mm [color="Infrared (880nm)" package="3 mm [THT]"]
  R7 = Resistor [tolerance=±5% resistance=220 package=THT]
  R8 = Resistor [tolerance=±5% resistance=220 package=THT]
  R9 = Resistor [tolerance=±5% resistance=220 package=THT]
  R10 = Resistor [tolerance=±5% resistance=10k package=THT]
  R11 = Resistor [tolerance=±5% resistance=10k package=THT]
  R12 = Resistor [tolerance=±5% resistance=10k package=THT]

nets:
  N1: Part1.OUT3, M1.pin_2
  N2: Part1.OUT4, M1.pin_1
  N3: Part1.OUT2, M2.pin_2
  N4: Part1.OUT1, M2.pin_1
  N5: Part1.5V, R10.Pin_1, R11.Pin_1, R12.Pin_1
  N6: Part1.A0, LED11.cathode, R11.Pin_0
  N7: Part1.A1, LED12.cathode, R12.Pin_0
  N8: Part1.A2, LED13.cathode, R10.Pin_0
  N9: Part1.D9, R7.Pin_1, R8.Pin_1, R9.Pin_1
  N10: Part1.GND, LED8.cathode, LED9.cathode, LED10.cathode, LED11.anode, LED12.anode, LED13.anode
  N11: LED8.anode, R8.Pin_0
  N12: LED9.anode, R7.Pin_0
  N13: LED10.anode, R9.Pin_0
