# Fritzing sketch id1524_Arduino_VoiceRecognition_0 (saved by Fritzing 0.8.7b)
breadboards: 1

parts:
  Componente1 = Arduino Uno (Rev3) - ICSP  # not connected
  U1 = XBee
  R1 = Resistor [tolerance=±5% resistance=10k package="0805 [SMD]"]
  R2 = Resistor [tolerance=±5% resistance=10k package="0805 [SMD]"]

nets:
  N1: U1.connector2, R1.Pin_1, R2.Pin_0
  N2: U1.connector9, R2.Pin_1

notes:
  R1 = R2 = 10k
  EASYVR Shild
  need to be mounted on an Arduino
