# Fritzing sketch id1525_PCBV2.3_0 (saved by Fritzing 0.9.2b)
circuit board: 4.17719cm x 6.94662cm
breadboards: 1

parts:
  Arduino_Nano = Arduino Nano (Rev3.0)
  R2-1k = Resistor [tolerance=±5% resistance=1k package=THT]
  R3-110k = Resistor [tolerance=±5% resistance=110k package=THT]
  R4-1M = Resistor [tolerance=±5% resistance=1M package=THT]
  Batt_+_- = Screw terminal - 2 pins [package=THT]
  CC_amp = Screw terminal - 2 pins [package=THT]
  R1-2k = Resistor [tolerance=±5% resistance=2k package=THT]
  Cont_Thr = Screw terminal - 2 pins [package=THT]
  HC-05 = Bluetooth HC-05 Macho

nets:
  GND: Arduino_Nano.GND, R3-110k.Pin_0, Batt_+_-.pin1, CC_amp.pin1, R1-2k.Pin_1, HC-05.GND
  N1: Arduino_Nano.D3, Cont_Thr.pin2
  N2: Arduino_Nano.D9, R2-1k.Pin_0
  N3: Arduino_Nano.D10, HC-05.TXD
  N4: Arduino_Nano.D11/MOSI, HC-05.Key
  N5: Arduino_Nano.D12/MISO, HC-05.VCC
  N6: Arduino_Nano.A2, Cont_Thr.pin1
  N7: Arduino_Nano.A1, CC_amp.pin2
  N8: Arduino_Nano.A0, R3-110k.Pin_1, R4-1M.Pin_0
  N9: R2-1k.Pin_1, R1-2k.Pin_0, HC-05.RXD
  N10: R4-1M.Pin_1, Batt_+_-.pin2

notes:
  François Boivin - ETrike throttle V1
