# Fritzing sketch id1528_EcoDuino_1_0 (saved by Fritzing 0.9.0b)
circuit board: 6.88566cm x 5.36311cm
breadboards: 1

parts:
  J11 = rounded female pin header, 8 pins [form="♀ (female rounded)"]
  J12 = rounded female pin header, 6 pins [form="♀ (female rounded)"]
  J13 = rounded female pin header, 8 pins [form="♀ (female rounded)"]
  BAT = Battery
  XTAL = Crystal [frequency="16 Mhz" package=THT]
  22pF = Capacitor [package=cap-pth-small2]
  22pF_2 = Capacitor [package=cap-pth-small2]
  10k = Resistor [tolerance=±5% resistance=10k package=THT]
  RST = Pushbutton [package="[THT]"]
  LED = LED - 5mm [color="Red (633nm)" package="5 mm [THT]"]
  1k = Resistor [tolerance=±5% resistance=1k package=THT]
  10uF = Electrolytic Capacitor [capacitance=10µF package="100 mil [THT, electrolytic]"]
  S = Toggle Switch [package=THT]
  D1 = Diode [package=diode-1n4001]
  J10 = rounded female pin header, 10 pins [form="♀ (female rounded)"]
  100nF = Ceramic Capacitor [capacitance=100nF package="100 mil [THT, multilayer]"]
  Plug = Power plug
  ISP = double row male pin header, 6 pins [form="♂ (male)"]
  J14 = male pin header, 6 pins [form="♂ (male)"]
  3V3 = Voltage Regulator [package=to220-igo]
  10uF_2 = Electrolytic Capacitor [capacitance=10µF package="100 mil [THT, electrolytic]"]
  10uF_3 = Electrolytic Capacitor [capacitance=10µF package="100 mil [THT, electrolytic]"]
  USB = USB connector [package=THT]
  10uF_4 = Electrolytic Capacitor [capacitance=10µF package="100 mil [THT, electrolytic]"]
  J15 = male pin header, 2 pins [form="♂ (male)"]
  J16 = male pin header, 2 pins [form="♂ (male)"]
  ATMEGA328P = atmega328 [package=dip]
  5V = Voltage Regulator [package=to220-igo]

nets:
  D7: J11.pin1, ATMEGA328P.D7
  D6: J11.pin2, ATMEGA328P.D6_(PWM)
  D5: J11.pin3, ATMEGA328P.D5_(PWM)
  D4: J11.pin4, ATMEGA328P.D4
  D3: J11.pin5, ATMEGA328P.D3_(PWM)
  D2: J11.pin6, ATMEGA328P.D2
  D1: J11.pin7, J14.pin2, ATMEGA328P.D1_(TX)
  D0: J11.pin8, J14.pin3, ATMEGA328P.D0_(RX)
  A0: J12.pin1, ATMEGA328P.A0
  A1: J12.pin2, ATMEGA328P.A1
  A2: J12.pin3, ATMEGA328P.A2
  A3: J12.pin4, ATMEGA328P.A3
  A4/SDA: J12.pin5, J10.pin2, ATMEGA328P.A4
  A5/SCL: J12.pin6, J10.pin1, ATMEGA328P.A5
  5V/AVCC/VCC: J13.pin2, J13.pin5, 10k.Pin_0, S.COM, ISP.pin6, J14.pin4, 10uF_2.+, ATMEGA328P.VCC, ATMEGA328P.AVCC
  RESET: J13.pin3, 10k.Pin_1, RST.Pin_3, 100nF.0, ISP.pin3, ATMEGA328P.RESET
  3V3: J13.pin4, J14.pin5, 3V3.OUT, 10uF_4.+
  GND: J13.pin6, J13.pin7, BAT.-, 22pF.1, 22pF_2.2, RST.Pin_1, RST.Pin_2, LED.cathode, 10uF.-, J10.pin4, Plug.GND, ISP.pin4, J14.pin6, 3V3.GND, 10uF_2.-, 10uF_3.-, USB.GND, USB.chassis5, 10uF_4.-, ATMEGA328P.GND, 5V.GND
  N1: J13.pin8, D1.C, Plug.VCC, J15.pin1, J16.pin1
  N2: BAT.+, D1.A
  N3: XTAL.pin_0, 22pF_2.1, ATMEGA328P.XLAT1
  N4: XTAL.pin_1, 22pF.2, ATMEGA328P.XLAT2
  N5: LED.anode, 1k.Pin_0
  D13: 1k.Pin_1, J10.pin5, ISP.pin2, ATMEGA328P.D13
  N6: 10uF.+, J16.pin2, 5V.IN
  N7: S.L1, USB.5V
  N8: S.L2, 5V.OUT
  AEREF pin: J10.pin3, ATMEGA328P.AREF
  D12: J10.pin6, ISP.pin1, ATMEGA328P.D12
  D11: J10.pin7, ISP.pin5, ATMEGA328P.D11_(PWM)
  D10: J10.pin8, ATMEGA328P.D10_(PWM)
  D9: J10.pin9, ATMEGA328P.D9_(PWM)
  D8: J10.pin10, ATMEGA328P.D8
  N9: 100nF.1, J14.pin1
  N10: 3V3.IN, 10uF_3.+, J15.pin2

notes:
  2016 v0.1
  by PAKOZM
  ALARDUINO
  2016 v1.1
  ECODUINO
  GND
  AREF
  7
  8
  ~9
  ~10
  ~6
  ~5
  4
  ~3
  2
  TX->1
  RX<-0
  ~11
  12
  13
  A4
  A3
  A2
  A0
  A1
  A5
  5V
  Vcc
  EcoDuino, Arduino with switchable voltage regulators., 1.1
  3v
  5v
  rx
  tx
  UART
  Vin
  Rst
  Reg
  USB
  ICSP
  .
  ISP
  :SDA
  SDA
  SCL
  rst
  gnd
  3V3
  IOREF
