# Fritzing sketch id1529_LCD_display_0 (saved by Fritzing 0.9.0b)
breadboards: 1

parts:
  ARDUINO = Arduino Uno (Rev3)
  Pot_(1_ou_10k) = Rotary Potentiometer (Small) [maximum_resistance=100kΩ package=THT]
  LCD1 = LCD screen

nets:
  N1: ARDUINO.D8, LCD1.DB5
  N2: ARDUINO.D9_PWM, LCD1.DB4
  N3: ARDUINO.D11_PWM/MOSI, LCD1.E
  N4: ARDUINO.D12/MISO, LCD1.RS
  GND: ARDUINO.GND, Pot_(1_ou_10k).leg1, LCD1.VSS, LCD1.R/W, LCD1.LED-
  N5: ARDUINO.D6_PWM, LCD1.DB7
  N6: ARDUINO.D7, LCD1.DB6
  5V: ARDUINO.5V, Pot_(1_ou_10k).leg2, LCD1.VDD, LCD1.LED+
  N7: Pot_(1_ou_10k).wiper, LCD1.V0
