# Fritzing sketch id152_4093_Quad_OSC_0 (saved by Fritzing 0.9.3b)
circuit board: 10cm x 10cm
breadboards: 1

parts:
  4093 = IC, DIP package, 14 pins [chip_label=IC]
  OSC1 = Electrolytic Capacitor [capacitance=1µF voltage=16V package="100 mil [THT, electrolytic]"]
  R1 = Resistor [tolerance=±5% resistance=1k package=THT]
  R1_2 = Rotary Potentiometer (Small) [maximum_resistance=100kΩ package=THT]
  OSC2 = Electrolytic Capacitor [capacitance=1µF voltage=16V package="100 mil [THT, electrolytic]"]
  R2 = Resistor [tolerance=±5% resistance=1k package=THT]
  R2_2 = Rotary Potentiometer (Small) [maximum_resistance=100kΩ package=THT]
  OSC3 = Electrolytic Capacitor [capacitance=1µF voltage=16V package="100 mil [THT, electrolytic]"]
  R3 = Resistor [tolerance=±5% resistance=1k package=THT]
  R3_2 = Rotary Potentiometer (Small) [maximum_resistance=100kΩ package=THT]
  OSC4 = Electrolytic Capacitor [capacitance=1µF voltage=16V package="100 mil [THT, electrolytic]"]
  R4 = Resistor [tolerance=±5% resistance=1k package=THT]
  R4_2 = Rotary Potentiometer (Small) [maximum_resistance=100kΩ package=THT]
  D4 = Rectifier Diode [part_number=1N4001 package="300 mil [THT]"]
  D1 = Rectifier Diode [part_number=1N4001 package="300 mil [THT]"]
  D2 = Rectifier Diode [part_number=1N4001 package="300 mil [THT]"]
  Out = Electrolytic Capacitor [capacitance=1µF package="100 mil [THT, electrolytic]"]
  U1 = AUDIO-JACK2 [package=audio-jack]
  D3 = Rectifier Diode [part_number=1N4001 package="300 mil [THT]"]
  Power = female pin header, 1 pin [form="♀ (female)"]
  Ground = female pin header, 1 pin [form="♀ (female)"]
  D5 = Rectifier Diode [part_number=1N4001 package="300 mil [THT]"]
  J1 = female pin header, 1 pin [form="♀ (female)"]
  J2 = female pin header, 16 pins [form="♀ (female)"]  # not connected
  J3 = female pin header, 16 pins [form="♀ (female)"]  # not connected
  J4 = female pin header, 16 pins [form="♀ (female)"]  # not connected
  J5 = female pin header, 16 pins [form="♀ (female)"]  # not connected
  J6 = female pin header, 16 pins [form="♀ (female)"]  # not connected
  J7 = female pin header, 16 pins [form="♀ (female)"]  # not connected
  J8 = female pin header, 10 pins [form="♀ (female)"]  # not connected
  J9 = female pin header, 10 pins [form="♀ (female)"]  # not connected
  J10 = female pin header, 10 pins [form="♀ (female)"]  # not connected
  J11 = female pin header, 10 pins [form="♀ (female)"]  # not connected
  J12 = female pin header, 10 pins [form="♀ (female)"]  # not connected
  J13 = female pin header, 10 pins [form="♀ (female)"]  # not connected
  J14 = female pin header, 10 pins [form="♀ (female)"]  # not connected
  J15 = female pin header, 10 pins [form="♀ (female)"]  # not connected
  J16 = female pin header, 10 pins [form="♀ (female)"]  # not connected
  J17 = female pin header, 10 pins [form="♀ (female)"]  # not connected
  J18 = female pin header, 16 pins [form="♀ (female)"]  # not connected
  J19 = female pin header, 16 pins [form="♀ (female)"]  # not connected
  J20 = female pin header, 14 pins [form="♀ (female)"]
  J21 = female pin header, 13 pins [form="♀ (female)"]  # not connected

nets:
  N1: 4093.pin1, 4093.pin2, OSC1.+, R1.Pin_1
  N2: 4093.pin3, R1_2.leg1, D1.anode
  N3: 4093.pin4, R2_2.wiper, D2.anode
  N4: 4093.pin5, 4093.pin6, OSC2.+, R2.Pin_0
  N5: 4093.pin7, OSC1.-, OSC2.-, OSC3.-, OSC4.-, U1.SLEEVE, Ground.pin1
  N6: 4093.pin8, 4093.pin9, OSC3.+, R3.Pin_0
  N7: 4093.pin10, R3_2.leg1, D3.anode
  N8: 4093.pin11, R4_2.wiper, D4.anode
  N9: 4093.pin12, 4093.pin13, OSC4.+, R4.Pin_1
  N10: 4093.pin14, Power.pin1, D5.cathode
  N11: R1.Pin_0, R1_2.wiper
  N12: R2.Pin_1, R2_2.leg1
  N13: R3.Pin_1, R3_2.wiper
  N14: R4.Pin_0, R4_2.leg1
  N15: D4.cathode, D1.cathode, D2.cathode, Out.+, D3.cathode
  N16: Out.-, U1.RING
  N17: D5.anode, J1.pin1
  N18: J20.pin11, J20.pin12
