# Fritzing sketch id1530_PrimeModule1_0 (saved by Fritzing 0.9.3b)
breadboards: 3

parts:
  Part1 = Arduino Uno (Rev3)  # not connected
  R1 = Resistor [tolerance=±5% resistance=220 package=THT]

nets:
  N1: R1.Pin_0, R1.Pin_1
