# Fritzing sketch id1531_EDGY_motor_control_two_motors_0 (saved by Fritzing 0.7.11b)
breadboards: 1

parts:
  Arduino1 = Arduino
  EDGY_motor_control = EDGY
  M1 = DC Motor
  M2 = DC Motor
  Power_plug1 = Power plug

nets:
  GND: Arduino1.GND, EDGY_motor_control.GND, Power_plug1.GND
  N1: Arduino1.D11, EDGY_motor_control.A1
  N2: Arduino1.D10, EDGY_motor_control.B1
  N3: Arduino1.D9, EDGY_motor_control.Speed1
  N4: Arduino1.D5, EDGY_motor_control.A2
  N5: Arduino1.D4, EDGY_motor_control.B2
  N6: Arduino1.D3, EDGY_motor_control.Speed2
  N7: Arduino1.+5V, EDGY_motor_control.5V+
  VIN: EDGY_motor_control.Vin, Power_plug1.VCC
  N8: EDGY_motor_control.B2out, M2.pin_2
  N9: EDGY_motor_control.A2out, M2.pin_1
  N10: EDGY_motor_control.B1out, M1.pin_2
  N11: EDGY_motor_control.A1out, M1.pin_1
