# Fritzing sketch id1532_EDGY_motor_control_stepper_0 (saved by Fritzing 0.7.11b)
breadboards: 1

parts:
  Arduino1 = Arduino
  EDGY_motor_control = EDGY
  Power_plug1 = Power plug
  M1 = Stepper Motor - Bipolar

nets:
  GND: Arduino1.GND, EDGY_motor_control.GND, Power_plug1.GND
  N1: Arduino1.D11, EDGY_motor_control.A1
  N2: Arduino1.D10, EDGY_motor_control.B1
  N3: Arduino1.D9, EDGY_motor_control.Speed1
  N4: Arduino1.D5, EDGY_motor_control.A2
  N5: Arduino1.D4, EDGY_motor_control.B2
  N6: Arduino1.D3, EDGY_motor_control.Speed2
  N7: Arduino1.+5V, EDGY_motor_control.5V+
  VIN: EDGY_motor_control.Vin, Power_plug1.VCC
  N8: EDGY_motor_control.B2out, M1.D
  N9: EDGY_motor_control.A2out, M1.B
  N10: EDGY_motor_control.B1out, M1.C
  N11: EDGY_motor_control.A1out, M1.A
