# Fritzing sketch id1533_official_edp_iot_hackathon_schema_0 (saved by Fritzing 0.9.3b)
breadboards: 1

parts:
  Akeru_3_3 = Arduino Uno (Rev3)
  U1 = MAX485 [package=dil08]
  R1 = Resistor [tolerance=±5% resistance=10k package="2010 [SMD]"]
  R2 = Resistor [tolerance=±5% resistance=10k package="2010 [SMD]"]

nets:
  N1: Akeru_3_3.D8, U1.RE, U1.DE
  N2: Akeru_3_3.D10_PWM/SS, U1.RO
  N3: Akeru_3_3.D11_PWM/MOSI, U1.DI
  5V: Akeru_3_3.5V, U1.VCC, R2.Pin_1
  GND: Akeru_3_3.GND, U1.GND, R1.Pin_0
  N4: U1.A, R2.Pin_0
  N5: U1.B, R1.Pin_1

notes:
  B
  GND
  +5V
  A
  Offical Schematic for the EDP IoT Hackathon 2017
  ---------------------------------------------------------------------
  The color of the wires are merely representative. You should only care about the RJ12 Connector Pin Labels.
  There are alternative ways to mount this circuit. This is just an example.
  Please be aware that the present schematic has 2 different types of power supply:
  1- Through the Arduino (via USB when connected to the PC)
  2- Through the EB
  ---------------------------------------------------------------------
  WARNING:
  - YOU SHOULD ALWAYS HAVE ONLY ONE POWER SUPPLY AT A TIME
  RJ12 Connector Pin Labels:
  Orange/White = A
  Blue/White = B
  Full Orange = GND
  Green/White = + 5 V
  The additional Full Blue & Full Green wires will not be used for the EDP IoT Hackathon
