# Fritzing sketch id1534_ee250_lab6_pcb_0 (saved by Fritzing 0.9.3b)
circuit board: 4cm x 4cm
breadboards: 1

parts:
  R1 = Resistor [tolerance=±5% resistance=220 package=THT]
  Sensor_1_(LED) = female pin header, 3 pins [form="♀ (female)"]
  Sensor_2 = female pin header, 3 pins [form="♀ (female)"]
  LED1 = LED - 3mm [color="Red (633nm)" package="3 mm [THT]"]
  MCP3008 = IC, DIP package, 16 pins [chip_label=IC]
  Addl_Chnls = female pin header, 4 pins [form="♀ (female)"]
  Grove1 = Grove Light Sensor
  Grove2 = Grove Light Sensor
  rPi_Pin_Out = double row female pin header, 26 pins [form="♀ (female)"]

nets:
  N1: R1.Pin_0, LED1.anode
  GND: R1.Pin_1, Sensor_1_(LED).pin1, Sensor_2.pin1, MCP3008.pin15, MCP3008.pin16, Grove1.GND, Grove2.GND, rPi_Pin_Out.pin24
  VCC: Sensor_1_(LED).pin2, Sensor_2.pin2, LED1.cathode, MCP3008.pin9, MCP3008.pin14, Grove1.VCC, Grove2.VCC, rPi_Pin_Out.pin1
  N2: Sensor_1_(LED).pin3, MCP3008.pin3
  N3: Sensor_2.pin3, MCP3008.pin4
  N4: MCP3008.pin1, Grove1.SIG
  N5: MCP3008.pin2, Grove2.SIG
  N6: MCP3008.pin5, Addl_Chnls.pin4
  N7: MCP3008.pin6, Addl_Chnls.pin3
  N8: MCP3008.pin7, Addl_Chnls.pin2
  N9: MCP3008.pin8, Addl_Chnls.pin1
  N10: MCP3008.pin10, rPi_Pin_Out.pin15
  N11: MCP3008.pin11, rPi_Pin_Out.pin10, rPi_Pin_Out.pin16
  N12: MCP3008.pin12, rPi_Pin_Out.pin11
  N13: MCP3008.pin13, rPi_Pin_Out.pin12
