# Fritzing sketch id1535_Final_Circuit_0 (saved by Fritzing 0.9.3b)
breadboards: 1

parts:
  V1 = DC Power [voltage=5]  # not connected
  U1 = OP27 - Low Noise, Precision Op Amp [part_number=OP27]
  10K_Potentiometer = POT [package=pot_alpha_rv16af-20]
  R1 = Resistor [tolerance=±5% resistance=100k package="1206 [SMD]"]
  Audio_Jack_Signal_Pin = Header 1 [package=1x01_offset]
  +5V = Header 1 [package=1x01_offset]
  Ground = Header 1 [package=1x01_offset]
  C1 = Electrolytic Capacitor [capacitance=10µF package="100 mil [THT, electrolytic]"]
  C2 = Ceramic Capacitor [capacitance=47nF package="100 mil [THT, multilayer]"]
  R2 = Resistor [tolerance=±5% resistance=100k package="1206 [SMD]"]
  R3 = Resistor [tolerance=±5% resistance=100k package="1206 [SMD]"]
  Audio_Jack_Ground_Pin = Header 1 [package=1x01_offset]
  C3 = Ceramic Capacitor [capacitance=100nF package="100 mil [THT, multilayer]"]
  R4 = Resistor [tolerance=±5% resistance=3.3k package="1206 [SMD]"]
  Q1 = Basic FET N-Channel [package="TO220 [THT]"]
  Q2 = Basic FET N-Channel [package="TO220 [THT]"]
  Q3 = Basic FET N-Channel [package="TO220 [THT]"]
  R5 = Resistor [tolerance=±5% resistance=220 package="2010 [SMD]"]
  -5V = Header 1 [package=1x01_offset]
  Ground_2 = Header 1 [package=1x01_offset]
  R6 = Resistor [tolerance=±5% resistance=220 package="2010 [SMD]"]
  R7 = Resistor [tolerance=±5% resistance=220 package="2010 [SMD]"]
  Part1 = Arduino Uno (Rev3) - ICSP

nets:
  N1: U1.-IN, 10K_Potentiometer.S, R1.Pin_1
  N2: U1.+IN, Audio_Jack_Signal_Pin.1
  N3: U1.-V, -5V.1
  N4: U1.OUT, R1.Pin_0, C1.-
  N5: U1.V+, +5V.1, R2.Pin_0
  N6: 10K_Potentiometer.A, Ground.1, C2.0, R3.Pin_0, Audio_Jack_Ground_Pin.1, C3.0
  N7: C1.+, C2.1, R2.Pin_1, R3.Pin_1, R4.Pin_0
  N8: C3.1, R4.Pin_1, Part1.A0
  N9: Q1.gate, R5.Pin_1
  N10: Q1.source, Q2.source, Q3.source, Ground_2.1
  N11: Q2.gate, R7.Pin_1
  N12: Q3.gate, R6.Pin_1
  N13: R5.Pin_0, Part1.D5_PWM
  N14: R6.Pin_0, Part1.D6_PWM
  N15: R7.Pin_0, Part1.D7

notes:
  The pin labels are for the Analog Discovery pinouts.
  Rotate potentiometer to adjust gain of the circuit as needed.
  LED Strip. Colors match, I.E. White to white green to green, etc.
  1/4" audio jack input
  Use LED strip's power supply for Arduino so that it may supply 9v from VIN
