# Fritzing sketch id1536_Non_Offset_Circuit_0 (saved by Fritzing 0.9.3b)
breadboards: 1

parts:
  V1 = DC Power [voltage=5]  # not connected
  U1 = OP27 - Low Noise, Precision Op Amp [part_number=OP27]
  10K_Potentiometer = POT [package=pot_alpha_rv16af-20]
  R1 = Resistor [tolerance=±5% resistance=100k package="1206 [SMD]"]
  -5V = Header 1 [package=1x01_offset]
  1+ = Header 1 [package=1x01_offset]
  W1 = Header 1 [package=1x01_offset]
  +5V = Header 1 [package=1x01_offset]
  Ground = Header 1 [package=1x01_offset]
  1- = Header 1 [package=1x01_offset]

nets:
  N1: U1.-IN, 10K_Potentiometer.S, R1.Pin_1
  N2: U1.+IN, W1.1
  N3: U1.-V, -5V.1
  N4: U1.OUT, R1.Pin_0, 1+.1
  N5: U1.V+, +5V.1
  N6: 10K_Potentiometer.A, Ground.1, 1-.1

notes:
  The pin labels are for the Analog Discovery pinouts when testing.
