# Fritzing sketch id1537_Offset_Circuit_0 (saved by Fritzing 0.9.3b)
breadboards: 1

parts:
  V1 = DC Power [voltage=5]  # not connected
  U1 = OP27 - Low Noise, Precision Op Amp [part_number=OP27]
  10K_Potentiometer = POT [package=pot_alpha_rv16af-20]
  R1 = Resistor [tolerance=±5% resistance=100k package="1206 [SMD]"]
  -5V = Header 1 [package=1x01_offset]
  1+ = Header 1 [package=1x01_offset]
  W1 = Header 1 [package=1x01_offset]
  +5V = Header 1 [package=1x01_offset]
  Ground = Header 1 [package=1x01_offset]
  1- = Header 1 [package=1x01_offset]
  2- = Header 1 [package=1x01_offset]
  2+ = Header 1 [package=1x01_offset]
  C1 = Electrolytic Capacitor [capacitance=10µF package="100 mil [THT, electrolytic]"]
  C2 = Ceramic Capacitor [capacitance=47nF package="100 mil [THT, multilayer]"]
  R2 = Resistor [tolerance=±5% resistance=100k package="1206 [SMD]"]
  R3 = Resistor [tolerance=±5% resistance=100k package="1206 [SMD]"]

nets:
  N1: U1.-IN, 10K_Potentiometer.S, R1.Pin_1
  N2: U1.+IN, W1.1
  N3: U1.-V, -5V.1
  N4: U1.OUT, R1.Pin_0, 1+.1, C1.-
  N5: U1.V+, +5V.1, R2.Pin_0
  N6: 10K_Potentiometer.A, Ground.1, 1-.1, 2-.1, C2.0, R3.Pin_0
  N7: 2+.1, C1.+, C2.1, R2.Pin_1, R3.Pin_1

notes:
  The pin labels are for the Analog Discovery pinouts when testing.
  Rotate potentiometer to adjust gain of the circuit as needed
