# Fritzing sketch id153_Music_BoxBackup_0 (saved by Fritzing 0.9.3b)
circuit board: 16cm x 10cm
breadboards: 2

parts:
  U1 = 555 Timer [package="DIP8 [THT]"]
  U2 = 555 Timer [package="DIP8 [THT]"]
  Power_plug1 = Power plug
  IC1 = IC, DIP package, 16 pins [chip_label=IC]
  R2 = Rotary Potentiometer (Large) [maximum_resistance=100kΩ package=THT]
  D1 = Rectifier Diode 10A [part_number=P1000K]
  D2 = Rectifier Diode 10A [part_number=P1000K]
  D3 = Rectifier Diode 10A [part_number=P1000K]
  D4 = Rectifier Diode 10A [part_number=P1000K]
  D5 = Rectifier Diode 10A [part_number=P1000K]
  D6 = Rectifier Diode 10A [part_number=P1000K]
  D7 = Rectifier Diode 10A [part_number=P1000K]
  D8 = Rectifier Diode 10A [part_number=P1000K]
  D9 = Rectifier Diode 10A [part_number=P1000K]
  D10 = Rectifier Diode 10A [part_number=P1000K]
  R3 = Rotary Potentiometer (Large) [maximum_resistance=100kΩ package=THT]
  R4 = Rotary Potentiometer (Large) [maximum_resistance=100kΩ package=THT]
  R5 = Rotary Potentiometer (Large) [maximum_resistance=100kΩ package=THT]
  R6 = Rotary Potentiometer (Large) [maximum_resistance=100kΩ package=THT]
  R7 = Rotary Potentiometer (Large) [maximum_resistance=100kΩ package=THT]
  R8 = Rotary Potentiometer (Large) [maximum_resistance=100kΩ package=THT]
  R9 = Rotary Potentiometer (Large) [maximum_resistance=100kΩ package=THT]
  R10 = Rotary Potentiometer (Large) [maximum_resistance=100kΩ package=THT]
  R11 = Rotary Potentiometer (Large) [maximum_resistance=100kΩ package=THT]
  R12 = Rotary Potentiometer (Large) [maximum_resistance=100kΩ package=THT]
  C2 = Ceramic Capacitor [capacitance=100nF package="200 mil [THT, multilayer]"]
  C1 = Capacitor Polarized [package=cpol-radial-10uf-25v]
  C3 = Capacitor Polarized [package=cpol-radial-10uf-25v]
  SP1 = SPEAKER [package=pcb_mount_speaker]
  R14 = Rotary Potentiometer (Large) [maximum_resistance=100kΩ package=THT]
  R1 = Resistor [tolerance=±5% resistance=1 package="1206 [SMD]"]
  R13 = Resistor [tolerance=±5% resistance=1 package="1206 [SMD]"]

nets:
  N1: U1.Ground, U2.Ground, Power_plug1.GND, C2.1, C1.-, SP1.+
  N2: U1.Trigger, U1.Threshold, C1.+, R1.Pin_1
  N3: U1.Output, R2.leg2
  N4: U1.Reset, U1.Vcc_Supply_Voltage, U2.Reset, U2.Vcc_Supply_Voltage, Power_plug1.VCC, IC1.pin16
  N5: U2.Trigger, U2.Threshold, C2.0, R13.Pin_1
  N6: U2.Output, C3.+, R14.leg2
  N7: U2.Control_Voltage, R3.leg2, R4.leg2, R5.leg2, R6.leg2, R7.leg2, R8.leg2, R9.leg2, R10.leg2, R11.leg2, R12.leg2
  N8: IC1.pin1, D6.anode
  N9: IC1.pin2, D2.anode
  N10: IC1.pin3, D1.anode
  N11: IC1.pin4, D3.anode
  N12: IC1.pin5, D7.anode
  N13: IC1.pin6, D8.anode
  N14: IC1.pin7, D4.anode
  N15: IC1.pin9, D9.anode
  N16: IC1.pin10, D5.anode
  N17: IC1.pin11, D10.anode
  N18: R2.wiper, R1.Pin_0
  N19: D1.cathode, R9.wiper
  N20: D2.cathode, R8.wiper
  N21: D3.cathode, R10.wiper
  N22: D4.cathode, R7.wiper
  N23: D5.cathode, R3.wiper
  N24: D6.cathode, R4.wiper
  N25: D7.cathode, R5.wiper
  N26: D8.cathode, R6.wiper
  N27: D9.cathode, R11.wiper
  N28: D10.cathode, R12.wiper
  N29: C3.-, SP1.-
  N30: R14.wiper, R13.Pin_0
