# Fritzing sketch id1542_egt_c_0 (saved by Fritzing 0.9.3b)
circuit board: 11.1185cm x 6.41262cm
breadboards: 1

parts:
  LCD_20x4 = LCD screen
  Componente1 = Arduino Uno (Rev3)
  R1 = Rotary Potentiometer (Small) [maximum_resistance=100kΩ package=THT]
  R2 = Resistor [tolerance=±5% resistance=220 package=THT]
  LED1 = smd LED [color="Red (633nm)" package="1206 [SMD]"]
  RHT1 = Humidity and Temperature Sensor RHT03
  S2 = Pushbutton [package="[THT]"]
  posteriore = MAX6675 [package=so08]
  anteriore = MAX6675 [package=so08]
  J1 = female pin header, 2 pins [form="♀ (female)"]
  J2 = female pin header, 2 pins [form="♀ (female)"]
  U2 = RELAY [package=relay-jzc]
  U3 = RELAY [package=relay-jzc]
  Power_plug1 = Power plug
  Power_plug2 = Power plug
  U4 = Luxeon LED [package=luxeon]
  J5 = Piezo Speaker

nets:
  VSS: LCD_20x4.VSS, LCD_20x4.R/W, LCD_20x4.LED-, Componente1.GND, R1.leg1, R2.Pin_0, RHT1.GND_1, S2.Pin_1, S2.Pin_2, posteriore.VSS, anteriore.VSS, U2.COIL2, U3.COIL2
  VDD: LCD_20x4.VDD, LCD_20x4.LED+, Componente1.5V, R1.leg2, RHT1.Vcc, posteriore.VDD, anteriore.VDD
  N1: LCD_20x4.V0, R1.wiper
  N2: LCD_20x4.RS, Componente1.D12/MISO
  N3: LCD_20x4.E, Componente1.D11_PWM/MOSI
  N4: LCD_20x4.DB4, Componente1.D5_PWM
  N5: LCD_20x4.DB5, Componente1.D4
  N6: LCD_20x4.DB6, Componente1.D3_PWM
  N7: LCD_20x4.DB7, Componente1.D2
  N8: Componente1.A0, U2.COIL1
  N9: Componente1.A1, U3.COIL1
  N10: Componente1.D8, posteriore.MISO, anteriore.MISO
  N11: Componente1.D9_PWM, anteriore.CS
  N12: Componente1.D10_PWM/SS, posteriore.SCK, anteriore.SCK
  N13: Componente1.D13/SCK, LED1.anode
  N14: Componente1.D6_PWM, posteriore.CS
  N15: Componente1.D7, RHT1.Data-signal
  N16: Componente1.RESET, S2.Pin_3, S2.Pin_4
  N17: R2.Pin_1, LED1.cathode
  N18: posteriore.T-, J2.pin1
  N19: posteriore.T+, J2.pin2
  N20: anteriore.T-, J1.pin1
  N21: anteriore.T+, J1.pin2
  N22: U2.NC, Power_plug2.VCC
  N23: U2.NO, U4.A
  N24: U3.NC, Power_plug1.VCC
  N25: U3.NO, J5.pin2
  N26: Power_plug1.GND, J5.pin1
  N27: Power_plug2.GND, U4.C
