# Fritzing sketch id1543_leds_0 (saved by Fritzing 0.9.2b)
circuit board: 8.46667cm x 5.64444cm
breadboards: 1

parts:
  Arduino = Arduino Uno (Rev3)
  LED_2 = LED - 5mm [color="Yellow (585nm)" package="5 mm [THT]"]
  R2 = Resistor [tolerance=±5% resistance=220 package=THT]
  LED_1 = LED - 5mm [color="Yellow (585nm)" package="5 mm [THT]"]
  R1 = Resistor [tolerance=±5% resistance=220 package=THT]
  LED_3 = LED - 5mm [color="Yellow (585nm)" package="5 mm [THT]"]
  R3 = Resistor [tolerance=±5% resistance=220 package=THT]
  LED_5 = LED - 5mm [color="Yellow (585nm)" package="5 mm [THT]"]
  R5 = Resistor [tolerance=±5% resistance=220 package=THT]
  LED_7 = LED - 5mm [color="Yellow (585nm)" package="5 mm [THT]"]
  R7 = Resistor [tolerance=±5% resistance=220 package=THT]
  LED_8 = LED - 5mm [color="Yellow (585nm)" package="5 mm [THT]"]
  R8 = Resistor [tolerance=±5% resistance=220 package=THT]
  LED_6 = LED - 5mm [color="Yellow (585nm)" package="5 mm [THT]"]
  R6 = Resistor [tolerance=±5% resistance=220 package=THT]
  LED_4 = LED - 5mm [color="Yellow (585nm)" package="5 mm [THT]"]
  R4 = Resistor [tolerance=±5% resistance=220 package=THT]

nets:
  N1: Arduino.D8, R6.Pin_1
  N2: Arduino.D9_PWM, R5.Pin_1
  N3: Arduino.D10_PWM/SS, R4.Pin_1
  N4: Arduino.D11_PWM/MOSI, R3.Pin_1
  N5: Arduino.D12/MISO, R2.Pin_1
  N6: Arduino.D13/SCK, R1.Pin_1
  N7: Arduino.GND, LED_2.cathode, LED_1.cathode, LED_3.cathode, LED_5.cathode, LED_7.cathode, LED_8.cathode, LED_6.cathode, LED_4.cathode
  N8: Arduino.D6_PWM, R8.Pin_1
  N9: Arduino.D7, R7.Pin_1
  N10: LED_2.anode, R2.Pin_0
  N11: LED_1.anode, R1.Pin_0
  N12: LED_3.anode, R3.Pin_0
  N13: LED_5.anode, R5.Pin_0
  N14: LED_7.anode, R7.Pin_0
  N15: LED_8.anode, R8.Pin_0
  N16: LED_6.anode, R6.Pin_0
  N17: LED_4.anode, R4.Pin_0
