# Fritzing sketch id1544_multiplexer_0 (saved by Fritzing 0.9.2b)
circuit board: 8.46667cm x 5.64444cm
breadboards: 1

parts:
  Arduino = Arduino Uno (Rev3)
  LED_2 = LED - 5mm [color="Yellow (585nm)" package="5 mm [THT]"]
  R2 = Resistor [tolerance=±5% resistance=220 package=THT]
  LED_1 = LED - 5mm [color="Yellow (585nm)" package="5 mm [THT]"]
  R1 = Resistor [tolerance=±5% resistance=220 package=THT]
  LED_3 = LED - 5mm [color="Yellow (585nm)" package="5 mm [THT]"]
  R3 = Resistor [tolerance=±5% resistance=220 package=THT]
  LED_5 = LED - 5mm [color="Yellow (585nm)" package="5 mm [THT]"]
  R5 = Resistor [tolerance=±5% resistance=220 package=THT]
  LED_7 = LED - 5mm [color="Yellow (585nm)" package="5 mm [THT]"]
  R7 = Resistor [tolerance=±5% resistance=220 package=THT]
  LED_8 = LED - 5mm [color="Yellow (585nm)" package="5 mm [THT]"]
  R8 = Resistor [tolerance=±5% resistance=220 package=THT]
  LED_6 = LED - 5mm [color="Yellow (585nm)" package="5 mm [THT]"]
  R6 = Resistor [tolerance=±5% resistance=220 package=THT]
  LED_4 = LED - 5mm [color="Yellow (585nm)" package="5 mm [THT]"]
  R4 = Resistor [tolerance=±5% resistance=220 package=THT]
  U1 = 74HC595 [package="DIP16 [THT]"]

nets:
  N1: Arduino.D8, U1.DS
  N2: Arduino.D12/MISO, U1.ST_CP
  GND: Arduino.GND, LED_2.cathode, LED_1.cathode, LED_3.cathode, LED_5.cathode, LED_7.cathode, LED_8.cathode, LED_6.cathode, LED_4.cathode, U1.GND
  N3: Arduino.D7, U1.SH_CP
  5V: Arduino.5V, U1.MR, U1.VCC
  N4: LED_2.anode, R2.Pin_0
  N5: R2.Pin_1, U1.Q1
  N6: LED_1.anode, R1.Pin_0
  N7: R1.Pin_1, U1.Q0
  N8: LED_3.anode, R3.Pin_0
  N9: R3.Pin_1, U1.Q2
  N10: LED_5.anode, R5.Pin_0
  N11: R5.Pin_1, U1.Q4
  N12: LED_7.anode, R7.Pin_0
  N13: R7.Pin_1, U1.Q6
  N14: LED_8.anode, R8.Pin_0
  N15: R8.Pin_1, U1.Q7
  N16: LED_6.anode, R6.Pin_0
  N17: R6.Pin_1, U1.Q5
  N18: LED_4.anode, R4.Pin_0
  N19: R4.Pin_1, U1.Q3
