# Fritzing sketch id1545_sketch_eindproject_lrjr3_0 (saved by Fritzing 0.9.3b)
breadboards: 1

parts:
  Part1 = Arduino Uno (Rev3)
  LED1 = LED - 5mm [color="Red (633nm)" package="5 mm [THT]"]
  LED2 = LED - 5mm [color="Green (555nm)" package="5 mm [THT]"]
  R1 = Resistor [tolerance=±5% resistance=330 package=THT]
  R2 = Resistor [tolerance=±5% resistance=330 package=THT]
  R3 = Photocell (LDR) [package=THT]
  R4 = Resistor [tolerance=±5% resistance=220 package=THT]
  T1 = LM35 Temperature Sensor [package="TO92 [THT]"]
  R5 = Resistor [tolerance=±5% resistance=220 package=THT]

nets:
  N1: Part1.A0, R3.pin_0
  N2: Part1.A1, T1.+Vs
  N3: Part1.D12/MISO, LED2.cathode
  N4: Part1.D13/SCK, LED1.cathode
  N5: Part1.5V, R4.Pin_1, R5.Pin_1
  GND: Part1.GND, R1.Pin_1, R2.Pin_1, R3.pin_1, R4.Pin_0, T1.GND, R5.Pin_0
  N6: LED1.anode, R1.Pin_0
  N7: LED2.anode, R2.Pin_0

notes:
  LM35 = Thermistor
