# Fritzing sketch id1546_Temperaturmelder_0 (saved by Fritzing 0.7.0b)
breadboards: 1

parts:
  T1 = LM35 Temperature Sensor [package="TO92 [THT]"]
  LED1 = LED - 5mm [color="Red (633nm)" package="5 mm [THT]"]
  R1 = Resistor [tolerance=±5% resistance=220 package=THT]
  LED2 = LED - 5mm [color="Green (560nm)" package="5 mm [THT]"]
  R2 = Resistor [tolerance=±5% resistance=220 package=THT]
  Arduino1 = Arduino

nets:
  N1: T1.+Vs, Arduino1.+5V
  N2: T1.Vout, Arduino1.A0
  GND: T1.GND, LED1.cathode, LED2.cathode, Arduino1.GND
  N3: LED1.anode, R1.Pin_0
  N4: R1.Pin_1, Arduino1.D12
  N5: LED2.anode, R2.Pin_0
  N6: R2.Pin_1, Arduino1.D11
