# Fritzing sketch id1547_Einparkhilfe_0 (saved by Fritzing 0.6.3b)
breadboards: 3

parts:
  U1 = 74HC595 [package="DIP16 [THT]"]
  U2 = 74HC595 [package="DIP16 [THT]"]
  Near_Pot = Rotary Potentiometer (Small) [maximum_resistance=100kΩ]
  Far_Pot = Rotary Potentiometer (Small) [maximum_resistance=100kΩ]
  Parallax_Ping))) = mystery part, 3 pins [chip_label=? spacing=300mil]
  LED1 = Red LED - 5mm [package="5 mm [THT]"]
  LED2 = Red LED - 5mm [package="5 mm [THT]"]
  LED3 = Red LED - 5mm [package="5 mm [THT]"]
  LED4 = yellow LED - 5mm [package="5 mm [THT]"]
  LED5 = yellow LED - 5mm [package="5 mm [THT]"]
  LED6 = yellow LED - 5mm [package="5 mm [THT]"]
  LED7 = green LED - 5mm [package="5 mm [THT]"]
  LED8 = green LED - 5mm [package="5 mm [THT]"]
  LED9 = green LED - 5mm [package="5 mm [THT]"]
  LED10 = yellow LED - 5mm [package="5 mm [THT]"]
  LED11 = yellow LED - 5mm [package="5 mm [THT]"]
  LED12 = yellow LED - 5mm [package="5 mm [THT]"]
  LED13 = Red LED - 5mm [package="5 mm [THT]"]
  LED14 = Red LED - 5mm [package="5 mm [THT]"]
  LED15 = Red LED - 5mm [package="5 mm [THT]"]
  R3 = Resistor [tolerance=±5% resistance=220 package=THT]
  R4 = Resistor [tolerance=±5% resistance=220 package=THT]
  R5 = Resistor [tolerance=±5% resistance=220 package=THT]
  R6 = Resistor [tolerance=±5% resistance=220 package=THT]
  R7 = Resistor [tolerance=±5% resistance=220 package=THT]
  R8 = Resistor [tolerance=±5% resistance=220 package=THT]
  R9 = Resistor [tolerance=±5% resistance=220 package=THT]
  R10 = Resistor [tolerance=±5% resistance=220 package=THT]
  R11 = Resistor [tolerance=±5% resistance=220 package=THT]
  R12 = Resistor [tolerance=±5% resistance=220 package=THT]
  R13 = Resistor [tolerance=±5% resistance=220 package=THT]
  R14 = Resistor [tolerance=±5% resistance=220 package=THT]
  R15 = Resistor [tolerance=±5% resistance=220 package=THT]
  R16 = Resistor [tolerance=±5% resistance=220 package=THT]
  R17 = Resistor [tolerance=±5% resistance=220 package=THT]
  Arduino = Arduino Nano v2.3

nets:
  N1: U1.Q1, R8.Pin_1
  N2: U1.Q2, R7.Pin_1
  N3: U1.Q3, R6.Pin_1
  N4: U1.Q4, R5.Pin_1
  N5: U1.Q5, R4.Pin_1
  N6: U1.Q6, R3.Pin_1
  GND: U1.GND, U1.OE, U2.GND, U2.OE, Near_Pot.leg1, Far_Pot.leg1, Parallax_Ping))).pin3, LED1.cathode, LED2.cathode, LED3.cathode, LED4.cathode, LED5.cathode, LED6.cathode, LED7.cathode, LED8.cathode, LED9.cathode, LED10.cathode, LED11.cathode, LED12.cathode, LED13.cathode, LED14.cathode, LED15.cathode, Arduino.GND
  5V: U1.MR, U1.VCC, U2.MR, U2.VCC, Near_Pot.leg2, Far_Pot.leg2, Parallax_Ping))).pin2, Arduino.+5V
  N7: U1.SH_CP, U2.SH_CP, Arduino.D12
  N8: U1.ST_CP, U2.ST_CP, Arduino.D8
  N9: U1.DS, U2.Q7'
  N10: U1.Q0, R9.Pin_1
  N11: U2.Q1, R16.Pin_1
  N12: U2.Q2, R15.Pin_1
  N13: U2.Q3, R14.Pin_1
  N14: U2.Q4, R13.Pin_1
  N15: U2.Q5, R12.Pin_1
  N16: U2.Q6, R11.Pin_1
  N17: U2.Q7, R10.Pin_1
  N18: U2.DS, Arduino.D11
  N19: U2.Q0, R17.Pin_1
  N20: Near_Pot.wiper, Arduino.A0
  N21: Far_Pot.wiper, Arduino.A1
  N22: Parallax_Ping))).pin1, Arduino.D4
  N23: LED1.anode, R3.Pin_0
  N24: LED2.anode, R4.Pin_0
  N25: LED3.anode, R5.Pin_0
  N26: LED4.anode, R6.Pin_0
  N27: LED5.anode, R7.Pin_0
  N28: LED6.anode, R8.Pin_0
  N29: LED7.anode, R9.Pin_0
  N30: LED8.anode, R10.Pin_0
  N31: LED9.anode, R11.Pin_0
  N32: LED10.anode, R12.Pin_0
  N33: LED11.anode, R13.Pin_0
  N34: LED12.anode, R14.Pin_0
  N35: LED13.anode, R15.Pin_0
  N36: LED14.anode, R16.Pin_0
  N37: LED15.anode, R17.Pin_0

notes:
  The mystery part is the parallax ping))) sensor. Look into the datasheed for the correct wiring.
