# Fritzing sketch id1549_E2_ESDigitales_0 (saved by Fritzing 0.9.2b)
circuit board: 8.46667cm x 5.64444cm
breadboards: 1

parts:
  Parte1 = Arduino Uno (Rev3)
  R1 = Resistor [tolerance=±5% resistance=470 package=THT]
  LED1 = LED - 5mm [color="Red (633nm)" package="5 mm [THT]"]
  S1 = Pushbutton [package="[THT]"]
  R2 = Resistor [tolerance=±5% resistance=470 package=THT]
  LED2 = LED - 5mm [color="Blue (430nm)" package="5 mm [THT]"]
  R3 = Resistor [tolerance=±5% resistance=470 package=THT]
  LED3 = LED - 5mm [color="Orange (605nm)" package="5 mm [THT]"]
  R4 = Resistor [tolerance=±5% resistance=470 package=THT]
  LED4 = LED - 5mm [color="Green (555nm)" package="5 mm [THT]"]
  R5 = Resistor [tolerance=±5% resistance=470 package=THT]
  LED5 = LED - 5mm [color="Yellow (574nm)" package="5 mm [THT]"]
  R6 = Resistor [tolerance=±5% resistance=10k package=THT]

nets:
  N1: Parte1.D8, R3.Pin_1
  N2: Parte1.D10_PWM/SS, R2.Pin_1
  N3: Parte1.D12/MISO, R1.Pin_1
  N4: Parte1.GND, LED1.cathode, LED2.cathode, LED3.cathode, LED4.cathode, LED5.cathode, R6.Pin_1
  N5: Parte1.D2, S1.Pin_1, S1.Pin_2, R6.Pin_0
  N6: Parte1.D4, R5.Pin_1
  N7: Parte1.D6_PWM, R4.Pin_1
  N8: Parte1.5V, S1.Pin_3, S1.Pin_4
  N9: R1.Pin_0, LED1.anode
  N10: R2.Pin_0, LED2.anode
  N11: R3.Pin_0, LED3.anode
  N12: R4.Pin_0, LED4.anode
  N13: R5.Pin_0, LED5.anode
