# Fritzing sketch id154_555POWLED_0 (saved by Fritzing 0.7.12b)
breadboards: 1

parts:
  P1 = Rotary Potentiometer (Small) [maximum_resistance=10kΩ]
  U1 = 555 Timer [package="DIP8 [THT]"]
  R1 = Resistor [tolerance=±5% resistance=1k package=THT]
  Q2 = NPN-Transistor [package="TO92 [THT]"]
  R2 = Resistor [tolerance=±5% resistance=10 package=THT]
  C1 = Electrolytic Capacitor [capacitance=1µF package="100 mil [THT, electrolytic]"]
  Q1 = Basic FET N-Channel [package="TO220 [THT]"]
  POW_LED_+_- = Screw terminal - 2 pins [package=THT]
  ControlLED = LED - 5mm [color="Yellow (595nm)" package="5 mm [THT]"]
  Power_plug = Power plug
  D1 = Schottky Diode [part_number=1N5817 package="300 mil [THT]"]
  D2 = Schottky Diode [part_number=1N5817 package="300 mil [THT]"]
  RS = Resistor [tolerance=±5% resistance=1 package=THT]

nets:
  N1: P1.leg1, D1.cathode
  N2: P1.wiper, U1.Trigger, U1.Threshold, C1.+
  N3: P1.leg2, D2.anode
  N4: U1.Ground, Q2.E, C1.-, Power_plug.GND, RS.Pin_1
  N5: U1.Output, R2.Pin_1
  N6: U1.Reset, U1.Vcc_Supply_Voltage, R1.Pin_0, POW_LED_+_-.pin1, ControlLED.anode, Power_plug.VCC
  N7: U1.Control_Voltage, Q2.C
  N8: U1.Discharge, D2.cathode
  N9: R1.Pin_1, D1.anode
  N10: Q2.B, Q1.source, RS.Pin_0
  N11: R2.Pin_0, Q1.gate
  N12: Q1.drain, POW_LED_+_-.pin2, ControlLED.cathode

notes:
  POW LED -  +
