# Fritzing sketch id1550_Sensor_Ultrasonico_Led_Zumbador_0 (saved by Fritzing 0.9.2b)
breadboards: 1

parts:
  LED1 = LED - 5mm [color="Red (633nm)" package="5 mm [THT]"]
  R1 = Resistor [tolerance=±5% resistance=330 package=THT]
  Parte1 = Arduino Uno (Rev3)
  J1 = Infrared Proximity Sensor

nets:
  N1: LED1.cathode, R1.Pin_1
  N2: LED1.anode, Parte1.D8
  N3: R1.Pin_0, Parte1.GND
  N4: Parte1.D12/MISO, J1.GND
  N5: Parte1.D13/SCK, J1.Vcc
  N6: Parte1.5V, J1.Vout
