# Fritzing sketch id1551_inicio_0 (saved by Fritzing 0.9.3b)
breadboards: 1

parts:
  Componente1 = Arduino Leonardo (Rev3b)
  S1 = Pushbutton [package="[THT]"]
  S2 = Pushbutton [package="[THT]"]
  J2 = Basic Servo
  LED1 = LED - 5mm [color="Red (633nm)" package="5 mm [THT]"]
  LED2 = LED - 5mm [color="Green (560nm)" package="5 mm [THT]"]
  J3 = Basic Servo

nets:
  N1: Componente1.D2/SDA, J3.pulse
  N2: Componente1.D3_PWM/SCL, LED2.anode
  N3: Componente1.D4/A6, J2.pulse
  N4: Componente1.D6_PWM/A7, LED1.anode
  VCC: Componente1.5V, J2.vcc, J3.vcc
  GND: Componente1.GND, J2.gnd, LED1.cathode, LED2.cathode, J3.gnd
  N5: S1.Pin_1, S1.Pin_2
  N6: S1.Pin_3, S1.Pin_4
  N7: S2.Pin_1, S2.Pin_2
  N8: S2.Pin_3, S2.Pin_4
