# Fritzing sketch id1552_ejerciciostaller_0 (saved by Fritzing 0.9.3b)
breadboards: 5

parts:
  LED1 = LED - 5mm [color="Red (633nm)" package="5 mm [THT]"]
  R1 = Resistor [tolerance=±5% resistance=1k package=THT]
  LED2 = LED - 5mm [color="Red (633nm)" package="5 mm [THT]"]
  R2 = Rotary Potentiometer (Large) [maximum_resistance=500k package=THT]
  R3 = Resistor [tolerance=±5% resistance=1k package=THT]
  R4 = Resistor [tolerance=±5% resistance=1k package=THT]
  R5 = Resistor [tolerance=±5% resistance=1k package=THT]
  LED3 = LED - 5mm [color="Red (633nm)" package="5 mm [THT]"]
  LED4 = LED - 5mm [color="Red (633nm)" package="5 mm [THT]"]
  R6 = Rotary Potentiometer (Large) [maximum_resistance=500k package=THT]
  R8 = Resistor [tolerance=±5% resistance=1k package=THT]
  R9 = Resistor [tolerance=±5% resistance=1k package=THT]
  LED5 = LED - 5mm [color="Red (633nm)" package="5 mm [THT]"]
  LED6 = LED - 5mm [color="Red (633nm)" package="5 mm [THT]"]
  R10 = Photocell (LDR) [package=THT]
  R11 = Photocell (LDR) [package=THT]
  LED7 = LED - 5mm [color="Red (633nm)" package="5 mm [THT]"]
  R12 = Resistor [tolerance=±5% resistance=100k package=THT]
  R13 = Resistor [tolerance=±5% resistance=4.7k package=THT]
  R14 = Photocell (LDR) [package=THT]
  R15 = Resistor [tolerance=±5% resistance=1k package=THT]
  Q1 = NPN-Transistor [package="TO92 [THT]"]
  VCC2 = Battery block 9V
  VCC1 = Battery block 9V
  VCC3 = Battery block 9V
  VCC4 = Battery block 9V
  VCC5 = Battery block 9V

nets (from the schematic view):
  N1: LED1.cathode, R1.Pin_1
  N2: LED1.anode, VCC1.+
  N3: R1.Pin_0, VCC1.-
  N4: LED2.cathode, R3.Pin_1
  N5: LED2.anode, R2.wiper
  N6: R2.leg2, VCC2.+
  N7: R3.Pin_0, VCC2.-
  N8: R4.Pin_0, LED3.cathode
  N9: R4.Pin_1, R5.Pin_1, VCC3.-
  N10: R5.Pin_0, LED4.cathode
  N11: LED3.anode, R6.leg2
  N12: LED4.anode, R6.leg1
  N13: R6.wiper, VCC3.+
  N14: R8.Pin_0, LED5.cathode
  N15: R8.Pin_1, R9.Pin_1, VCC4.-
  N16: R9.Pin_0, LED6.cathode
  N17: LED5.anode, R10.pin_1
  N18: LED6.anode, R11.pin_1
  N19: R10.pin_0, R11.pin_0, VCC4.+
  N20: LED7.cathode, Q1.C
  N21: LED7.anode, R15.Pin_0
  N22: R12.Pin_0, R15.Pin_1, VCC5.+
  N23: R12.Pin_1, R13.Pin_0, R14.pin_0
  N24: R13.Pin_1, Q1.B
  N25: R14.pin_1, Q1.E, VCC5.-
