# Fritzing sketch id1553_ekran_0 (saved by Fritzing 0.9.3b)
breadboards: 1

parts:
  LCD1 = LCD screen
  Part1 = Arduino Uno (Rev3)
  R1 = Trimmer Potentiometer [maximum_resistance=10kΩ package=THT]

nets:
  VSS: LCD1.VSS, LCD1.R/W, LCD1.LED-, Part1.GND, R1.leg1
  VDD: LCD1.VDD, LCD1.LED+, Part1.5V, R1.leg2
  N1: LCD1.V0, R1.wiper
  N2: LCD1.RS, Part1.D12/MISO
  N3: LCD1.E, Part1.D11_PWM/MOSI
  N4: LCD1.DB4, Part1.D10_PWM/SS
  N5: LCD1.DB5, Part1.D9_PWM
  N6: LCD1.DB6, Part1.D8
  N7: LCD1.DB7, Part1.D7
