# Fritzing sketch id1554_percy_proyecto_0 (saved by Fritzing 0.7.5b)
breadboards: 1

parts:
  Arduino1 = Arduino
  R2 = Resistor [tolerance=±5% resistance=220 package=THT]
  R3 = Resistor [tolerance=±5% resistance=220 package=THT]
  LED2 = LED - 5mm [color="Red (633nm)" package="5 mm [THT]"]
  LED3 = LED - 5mm [color="Red (633nm)" package="5 mm [THT]"]
  J1 = Piezo Speaker

nets:
  N1: Arduino1.D3, LED2.cathode
  N2: Arduino1.D2, LED3.cathode
  N3: Arduino1.3V3, R2.Pin_1, R3.Pin_1, J1.pin1
  N4: Arduino1.GND, J1.pin2
  N5: R2.Pin_0, LED2.anode
  N6: R3.Pin_0, LED3.anode
