# Fritzing sketch id1555_ARDUINO_KATTY_0 (saved by Fritzing 0.7.5b)
breadboards: 1

parts:
  Arduino1 = Arduino
  S1 = Pushbutton [package="[THT]"]
  LED1 = LED - 5mm [color="Red (633nm)" package="5 mm [THT]"]
  R1 = Resistor [tolerance=±5% resistance=220 package=THT]
  R2 = Resistor [tolerance=±5% resistance=220 package=THT]
  R3 = Resistor [tolerance=±5% resistance=220 package=THT]
  R4 = Resistor [tolerance=±5% resistance=220 package=THT]
  LED2 = LED - 5mm [color="Yellow (585nm)" package="5 mm [THT]"]
  LED3 = LED - 5mm [color="Green (555nm)" package="5 mm [THT]"]
  R5 = Resistor [tolerance=±5% resistance=220 package=THT]
  R6 = Resistor [tolerance=±5% resistance=220 package=THT]
  LED4 = LED - 5mm [color="Red (633nm)" package="5 mm [THT]"]
  LED5 = LED - 5mm [color="Yellow (585nm)" package="5 mm [THT]"]
  R7 = Resistor [tolerance=±5% resistance=220 package=THT]  # not connected
  LED6 = LED - 5mm [color="Green (555nm)" package="5 mm [THT]"]

nets:
  N1: Arduino1.D8, S1.Pin_3, S1.Pin_4, R1.Pin_1
  N2: Arduino1.D7, R2.Pin_1
  N3: Arduino1.D6, R3.Pin_1
  N4: Arduino1.D5, R4.Pin_1
  N5: Arduino1.D3, R6.Pin_1
  N6: Arduino1.+5V, LED1.cathode, R1.Pin_0, LED2.cathode, LED3.cathode, LED4.cathode, LED5.cathode, LED6.cathode
  N7: Arduino1.GND, S1.Pin_1, S1.Pin_2
  N8: R3.Pin_0, LED2.anode
  N9: R4.Pin_0, LED3.anode
  N10: R5.Pin_0, LED4.anode
  N11: R6.Pin_0, LED5.anode
