# Fritzing sketch id1558_fritzing_sketch_0 (saved by Fritzing 0.9.3b)
breadboards: 1

parts:
  Part2 = adafruit [part_number="Adafruit #2542"]
  Part3 = Arduino Mega 2560 (Rev3)
  S2 = Momentary Switch [package=ksa_sealed_tac_switch]
  LED1 = smd LED [color="Red (633nm)" package="0805 [SMD]"]
  R1 = Resistor [tolerance=±5% resistance=220 package=THT]

nets:
  N1: Part2.connector90, Part2.connector93, Part3.5V
  N2: Part2.connector92, Part2.connector98, Part3.GND, S2.1, R1.Pin_1
  N3: Part2.connector94, Part3.D4_PWM
  N4: Part2.connector95, Part3.D10_PWM
  N5: Part2.connector96, Part3.D11_PWM
  N6: Part3.D6_PWM, LED1.anode
  N7: Part3.D7_PWM, S2.4
  N8: LED1.cathode, R1.Pin_0
