# Fritzing sketch id1559_Basic_OpAmp_0 (saved by Fritzing 0.6.3b)
breadboards: 1

parts:
  Arduino1 = Arduino
  U2 = LM 358 Dual Op-Amp [package="DIP8 [THT]"]
  MIC2 = Microphone
  R6 = Trimmer Potentiometer [maximum_resistance=100kΩ package=THT]
  R7 = Resistor [tolerance=±5% resistance=10k package=THT]
  R8 = Resistor [tolerance=±5% resistance=10k package=THT]
  R9 = Resistor [tolerance=±5% resistance=1k package=THT]
  R10 = Resistor [tolerance=±5% resistance=10k package=THT]
  C3 = Electrolytic Capacitor [capacitance=0.1µF package="100 mil [THT, electrolytic]"]
  C4 = Electrolytic Capacitor [capacitance=4.7µF package="100 mil [THT, electrolytic]"]
  TRS2 = Stereo Jack (TRS) 3.5mm [package="PG203J [THT]"]

nets:
  N1: Arduino1.GND, U2.connector3, TRS2.Sleeve
  N2: Arduino1.+5V, U2.connector7, R7.Pin_1, R10.Pin_0
  N3: Arduino1.A1, C4.-, TRS2.Ring, TRS2.Tip
  N4: U2.connector0, R6.leg1, R6.wiper, C4.+
  N5: U2.connector1, R6.leg2, R9.Pin_1
  N6: U2.connector2, R7.Pin_0, R8.Pin_0
  N7: MIC2.pin1, R8.Pin_1
  N8: MIC2.pin2, R10.Pin_1, C3.+
  N9: R9.Pin_0, C3.-
