# Fritzing sketch id155_LED_Matrix (saved by Fritzing 0.5.2b)
breadboards: 6

parts:
  Nano1 = Arduino Nano v2.3
  IC1 = IC, DIP package, 28 pins [chip_label=TLC5940 spacing=300mil]
  C2 = Ceramic Capacitor [capacitance=0.1µF rated_voltage=35V package="100 mil [THT, multilayer]"]
  C3 = Electrolytic Capacitor [capacitance=100µF rated_voltage=35V package="100 mil [THT, electrolytic]"]
  R1 = Resistor [resistance=1.8k package=THT]
  Q1 = Basic FET P-Channel [package="TO220 [THT]"]
  Q1_2 = Basic FET P-Channel [package="TO220 [THT]"]
  Q1_3 = Basic FET P-Channel [package="TO220 [THT]"]
  Q1_4 = Basic FET P-Channel [package="TO220 [THT]"]
  R2 = Resistor [resistance=4.7k package=THT]
  LED1 = RGB LED - (4 legs) [package="5 mm [THT]"]
  LED1_2 = RGB LED - (4 legs) [package="5 mm [THT]"]
  LED1_3 = RGB LED - (4 legs) [package="5 mm [THT]"]
  LED1_4 = RGB LED - (4 legs) [package="5 mm [THT]"]
  R2_2 = Resistor [resistance=4.7k package=THT]
  R2_3 = Resistor [resistance=4.7k package=THT]
  R2_4 = Resistor [resistance=4.7k package=THT]
  LED1_5 = RGB LED - (4 legs) [package="5 mm [THT]"]
  LED1_6 = RGB LED - (4 legs) [package="5 mm [THT]"]
  LED1_7 = RGB LED - (4 legs) [package="5 mm [THT]"]
  LED1_8 = RGB LED - (4 legs) [package="5 mm [THT]"]
  LED1_9 = RGB LED - (4 legs) [package="5 mm [THT]"]
  LED1_10 = RGB LED - (4 legs) [package="5 mm [THT]"]
  LED1_11 = RGB LED - (4 legs) [package="5 mm [THT]"]
  LED1_12 = RGB LED - (4 legs) [package="5 mm [THT]"]
  LED1_13 = RGB LED - (4 legs) [package="5 mm [THT]"]
  LED1_14 = RGB LED - (4 legs) [package="5 mm [THT]"]
  LED1_15 = RGB LED - (4 legs) [package="5 mm [THT]"]
  LED1_16 = RGB LED - (4 legs) [package="5 mm [THT]"]

nets:
  N1: Nano1.GND, IC1.pin22, C2.1, C3.-, R1.Pin_0
  N2: Nano1.D2, Q1.gate, R2.Pin_0
  N3: Nano1.D3, IC1.pin18
  N4: Nano1.D4, IC1.pin26
  N5: Nano1.D6, IC1.pin25
  N6: Nano1.D7, Q1_3.gate, R2_3.Pin_0
  N7: Nano1.D8, Q1_2.gate, R2_2.Pin_0
  N8: Nano1.D9, IC1.pin24
  N9: Nano1.D10, IC1.pin23
  N10: Nano1.D11, Q1_4.gate, R2_4.Pin_0
  N11: Nano1.D12, IC1.pin27
  N12: Nano1.+5V, IC1.pin19, IC1.pin21, C2.0, C3.+, Q1.source, Q1_2.source, Q1_3.source, Q1_4.source, R2.Pin_1, R2_2.Pin_1, R2_3.Pin_1, R2_4.Pin_1
  N13: IC1.pin20, R1.Pin_1
  N14: Q1.drain, LED1.common_anode, LED1_2.common_anode, LED1_3.common_anode, LED1_4.common_anode
  N15: Q1_2.drain, LED1_5.common_anode, LED1_6.common_anode, LED1_7.common_anode, LED1_8.common_anode
  N16: Q1_3.drain, LED1_9.common_anode, LED1_14.common_anode, LED1_15.common_anode, LED1_16.common_anode
  N17: Q1_4.drain, LED1_10.common_anode, LED1_11.common_anode, LED1_12.common_anode, LED1_13.common_anode
