# Fritzing sketch id1560_Gen_LA_298_0_Schematic_1_0 (saved by Fritzing 0.8.7b)
breadboards: 1

parts:
  U1 = LM386 [part_number=LM386 package=dip08]
  MIC1 = Microphone
  SPKR1 = Loudspeaker
  C1 = Electrolytic Capacitor [capacitance=100µF package="100 mil [THT, electrolytic]"]
  R1 = Resistor [tolerance=±5% resistance=10k package=THT]
  C3 = Electrolytic Capacitor [capacitance=0.1µF package="100 mil [THT, electrolytic]"]
  VCC1 = Battery block 9V
  R2 = Resistor [tolerance=±5% resistance=10k package=THT]
  R3 = Resistor [tolerance=±5% resistance=10k package=THT]
  R4 = Resistor [tolerance=±5% resistance=330k package=THT]
  R5 = Resistor [tolerance=±5% resistance=10k package=THT]
  C4 = Ceramic Capacitor [capacitance=100nF package="100 mil [THT, multilayer]"]
  C2 = Ceramic Capacitor [capacitance=100nF package="100 mil [THT, multilayer]"]
  C5 = Ceramic Capacitor [capacitance=100nF package="100 mil [THT, multilayer]"]
  Q1 = NPN-Transistor [part_number=2N3904 package="TO92 [THT]"]

nets:
  N1: U1.GAIN, C3.-, C3.+
  N2: U1.-IN, U1.V-, MIC1.pin1, SPKR1.pin1, R1.Pin_0, VCC1.-, R2.Pin_0, Q1.E
  N3: U1.+IN, C4.0
  N4: U1.OUT, C1.-, C2.0
  N5: U1.V+, VCC1.+, R3.Pin_0, R5.Pin_0
  N6: U1.BP, R1.Pin_1
  N7: MIC1.pin2, R3.Pin_1, C5.1
  N8: SPKR1.pin2, C1.+
  N9: R2.Pin_1, C2.1
  N10: R4.Pin_0, R5.Pin_1, C4.1, Q1.C
  N11: R4.Pin_1, C5.0, Q1.B
