# Fritzing sketch id1561_konstlast_0 (saved by Fritzing 0.8.3b)
circuit board: 10cm x 6cm

parts:
  C1 = Ceramic Capacitor [capacitance=100nF package="100 mil [THT, multilayer]"]
  Q1 = Basic FET P-Channel [package="TO220 [THT]"]
  J1 = Screw terminal - 2 pins [package=THT]
  R2 = Resistor [tolerance=±5% resistance=220 package=THT]
  R3 = Resistor [tolerance=±5% resistance=220 package="1206 [SMD]"]
  U1 = LM 358 Dual Op-Amp [package="SO 08 [SMD]"]
  R1 = Rotary Potentiometer (Small) [maximum_resistance=100kΩ]
  RaspberryPi2 = Raspberry_Pi_Model_B
  IC1 = SOIC-14 [chip_label=ADC part_number=3004 package=SO]

nets:
  GND: C1.0, R3.Pin_1, U1.connector3, R1.leg2, RaspberryPi2.connector6
  N1: C1.1, R2.Pin_0, U1.connector2
  N2: Q1.gate, U1.connector0
  N3: Q1.drain, J1.pin1, IC1.3
  N4: Q1.source, R3.Pin_0, U1.connector1, IC1.2
  N5: R2.Pin_1, RaspberryPi2.connector12
  N6: U1.connector7, R1.leg1, RaspberryPi2.connector2, IC1.14
  N7: R1.wiper, IC1.1
  N8: RaspberryPi2.connector19, IC1.9
  N9: RaspberryPi2.connector21, IC1.10
  N10: RaspberryPi2.connector24, IC1.8
