# Fritzing sketch id1562_autolock_project_0 (saved by Fritzing 0.9.3b)
circuit board: 7.83649cm x 6.49719cm
breadboards: 1

parts:
  Componente1 = Arduino Uno (Rev3) - ICSP
  IR1 = TSOP312.., 314.. [package=THT]
  IR2 = TSOP312.., 314.. [package=THT]
  Lcd = LCD-16X2 [package=lcd-16x2_noholes]
  110 = Resistor [tolerance=±5% resistance=110 package=THT]
  J1 = Piezo Speaker
  R1 = Resistor [tolerance=±5% resistance=220 package=THT]
  2_2k = Resistor [tolerance=±5% resistance=2.21k package=THT]
  10k = Resistor [tolerance=±5% resistance=10k package=THT]
  110_2 = Resistor [tolerance=±5% resistance=110 package=THT]
  S1 = Momentary Switch [package=ksa_sealed_tac_switch]
  Servo = Dagu DGServo 9g (Top view) [part_number=RS001B]

nets:
  5V: Componente1.5V, IR1.Vs, IR2.Vs, Lcd.VDD, Lcd.R_W, S1.4
  GND: Componente1.GND, IR1.GND, IR2.GND, Lcd.VSS, 2_2k.Pin_1, 10k.Pin_0, 110_2.Pin_1, Servo.gnd
  N1: Componente1.D8, S1.1
  N2: Componente1.D9_PWM, J1.pin2
  N3: Componente1.D10_PWM/SS, R1.Pin_0
  N4: Componente1.D11_PWM/MOSI, Lcd.E
  N5: Componente1.D12/MISO, Lcd.RS
  N6: Componente1.D2, Lcd.DB4
  N7: Componente1.D3_PWM, Lcd.DB5
  N8: Componente1.D4, Lcd.DB6
  N9: Componente1.D5_PWM, Lcd.DB7
  N10: Componente1.D6_PWM, 110.Pin_1
  9V: Componente1.VIN, Servo.vcc
  N11: IR1.Data, IR2.Data, 110.Pin_0
  N12: Lcd.VO, 2_2k.Pin_0
  N13: J1.pin1, 110_2.Pin_0
  N14: R1.Pin_1, Servo.pulse
  N15: 10k.Pin_1, S1.2

notes:
  Padrão de cores:
  preto - GND
  vermelho - 5V
  Vermelho c/ listras - VIn
  Cores dos componentes:
  verde - Ir Receiver
  Amarelo - Lcd/Write pins
  Azul - Lcd/data pins
  cinza - Lcd/ dead pins
  Sabre de luz luke Ep. IV - Button
  laranja - buzzer
  branco - servomotor pwm pulse
  pendragon
  autolock
  project
  V 1.0
  Mod 2
