# Fritzing sketch id1563_hmc5883l_0 (saved by Fritzing 0.9.3b)
circuit board: 5.64444cm x 8.46667cm
breadboards: 1

parts:
  MEGA_1 = Arduino Mega 2560 (Rev3)
  Componente1 = Triple Axis Magnetometer - HMC5883 Breakout

nets (from the pcb view):
  N1: MEGA_1.connector46, Componente1.SCL
  N2: MEGA_1.connector47, Componente1.SDA
  N3: MEGA_1.connector257, Componente1.VCC
  N4: MEGA_1.connector260, Componente1.GND
