# Fritzing sketch id1564_Padlock_3.0_0 (saved by Fritzing 0.9.2b)
breadboards: 1

parts:
  Part1 = Arduino Uno (Rev3)
  LCD1 = LCD screen
  R1 = Resistor [tolerance=±5% resistance=220 package=THT]
  S1 = Pushbutton [package="[SMD]"]
  S2 = Pushbutton [package="[SMD]"]
  S3 = Pushbutton [package="[SMD]"]
  S4 = Pushbutton [package="[SMD]"]
  S5 = Pushbutton [package="[SMD]"]
  S6 = Pushbutton [package="[SMD]"]
  C1 = Electrolytic Capacitor [capacitance=1μF package="0405 [SMD, electrolytic]"]
  J1 = Basic Servo

nets:
  N1: Part1.A1, J1.pulse
  N2: Part1.D8, LCD1.DB5
  N3: Part1.D9_PWM, LCD1.DB4
  N4: Part1.D10_PWM/SS, S5.Pin_3, S5.Pin_4
  N5: Part1.D11_PWM/MOSI, LCD1.E
  N6: Part1.D12/MISO, LCD1.RS
  N7: Part1.D13/SCK, S6.Pin_3, S6.Pin_4
  GND: Part1.GND, LCD1.VSS, LCD1.V0, LCD1.R/W, LCD1.LED-, S1.Pin_1, S1.Pin_2, S2.Pin_1, S2.Pin_2, S3.Pin_1, S3.Pin_2, S4.Pin_1, S4.Pin_2, S5.Pin_1, S5.Pin_2, S6.Pin_1, S6.Pin_2, C1.-, J1.gnd
  N8: Part1.D2, S1.Pin_3, S1.Pin_4
  N9: Part1.D3_PWM, S2.Pin_3, S2.Pin_4
  N10: Part1.D4, S3.Pin_3, S3.Pin_4
  N11: Part1.D5_PWM, S4.Pin_3, S4.Pin_4
  N12: Part1.D6_PWM, LCD1.DB7
  N13: Part1.D7, LCD1.DB6
  5V: Part1.5V, LCD1.VDD, R1.Pin_0, C1.+, J1.vcc
  N14: LCD1.LED+, R1.Pin_1
