# Fritzing sketch id1567_mpb_pcb_layout_v01_01_04_0 (saved by Fritzing 0.9.2b)
circuit board: 17.78cm x 11.43cm
breadboards: 1

parts:
  X7 = screw terminal, 2 pins
  X8 = screw terminal, 2 pins
  X9 = screw terminal, 2 pins
  U3 = IC, DIP package, 40 pins [chip_label=IC]
  U1 = IC, DIP package, 40 pins [chip_label=IC]
  U2 = IC, DIP package, 40 pins [chip_label=IC]
  U5 = IC, DIP package, 22 pins [chip_label=IC]
  U4 = IC, DIP package, 22 pins [chip_label=IC]
  C1 = screw terminal, 2 pins
  R24 = Resistor [tolerance=±5% resistance=220 package=THT]
  R26 = Resistor [tolerance=±5% resistance=220 package=THT]
  R25 = Resistor [tolerance=±5% resistance=220 package=THT]
  R29 = Resistor [tolerance=±5% resistance=220 package=THT]
  R30 = Resistor [tolerance=±5% resistance=220 package=THT]
  R31 = Resistor [tolerance=±5% resistance=220 package=THT]
  R32 = Resistor [tolerance=±5% resistance=220 package=THT]
  R27 = Resistor [tolerance=±5% resistance=220 package=THT]
  R28 = Resistor [tolerance=±5% resistance=220 package=THT]
  R1 = Resistor [tolerance=±5% resistance=220 package=THT]
  R2 = Resistor [tolerance=±5% resistance=220 package=THT]
  R3 = Resistor [tolerance=±5% resistance=220 package=THT]
  R4 = Resistor [tolerance=±5% resistance=220 package=THT]
  C2 = screw terminal, 2 pins
  R5 = Resistor [tolerance=±5% resistance=220 package=THT]
  R6 = Resistor [tolerance=±5% resistance=220 package=THT]
  R7 = Resistor [tolerance=±5% resistance=220 package=THT]
  R8 = Resistor [tolerance=±5% resistance=220 package=THT]
  R9 = Resistor [tolerance=±5% resistance=220 package=THT]
  R10 = Resistor [tolerance=±5% resistance=220 package=THT]
  R12 = Resistor [tolerance=±5% resistance=220 package=THT]
  R13 = Resistor [tolerance=±5% resistance=220 package=THT]
  R11 = Resistor [tolerance=±5% resistance=220 package=THT]
  R15 = Resistor [tolerance=±1% resistance=220 package=THT]
  R14 = Resistor [tolerance=±5% resistance=220 package=THT]
  R16 = Resistor [tolerance=±5% resistance=220 package=THT]
  R17 = Resistor [tolerance=±5% resistance=220 package=THT]
  R18 = Resistor [tolerance=±5% resistance=220 package=THT]
  R19 = Resistor [tolerance=±5% resistance=220 package=THT]
  R20 = Resistor [tolerance=±5% resistance=220 package=THT]
  R23 = Resistor [tolerance=±5% resistance=220 package=THT]
  R22 = Resistor [tolerance=±5% resistance=220 package=THT]
  R21 = Resistor [tolerance=±5% resistance=220 package=THT]
  U9 = IC, DIP package, 8 pins [chip_label=IC]
  U6 = IC, DIP package, 14 pins [chip_label=IC]
  U7 = IC, DIP package, 8 pins [chip_label=IC]
  U8 = IC, DIP package, 8 pins [chip_label=IC]
  U12 = IC, DIP package, 8 pins [chip_label=IC]
  U11 = IC, DIP package, 8 pins [chip_label=IC]
  U13 = IC, DIP package, 8 pins [chip_label=IC]
  U10 = IC, DIP package, 8 pins [chip_label=IC]
  X4 = screw terminal, 2 pins
  X5 = screw terminal, 2 pins
  X6 = screw terminal, 2 pins

nets:
  N1: X7.pin1, C1.pin2
  N2: X7.pin2, U12.pin8
  N3: X8.pin1, U7.pin4
  N4: X8.pin2, U7.pin1, U8.pin8
  N5: X9.pin2, U5.pin2, U4.pin2, R12.Pin_0, R13.Pin_0, R11.Pin_0, U10.pin8
  N6: U3.pin1, R4.Pin_0
  N7: U3.pin2, R3.Pin_0
  N8: U3.pin9, U3.pin10, U2.pin29, R25.Pin_0, C2.pin2, U12.pin1, U12.pin2, U12.pin3, U12.pin4, U12.pin7
  N9: U3.pin12, U3.pin32, R24.Pin_0, R22.Pin_1, R21.Pin_1
  N10: U3.pin23, R23.Pin_1, X4.pin1
  N11: U3.pin24, U8.pin7
  N12: U3.pin25, U8.pin6
  N13: U3.pin26, U8.pin5
  N14: U3.pin29, U8.pin4
  N15: U3.pin36, U8.pin1
  N16: U3.pin37, R21.Pin_0, U12.pin6
  N17: U3.pin38, R22.Pin_0, U12.pin5
  N18: U1.pin1, R9.Pin_0
  N19: U1.pin2, R10.Pin_0
  N20: U1.pin3, R5.Pin_0
  N21: U1.pin4, R6.Pin_0
  N22: U1.pin5, R7.Pin_0
  N23: U1.pin6, R8.Pin_0
  N24: U1.pin9, U1.pin10, U10.pin1, U10.pin2, U10.pin3, U10.pin4, U10.pin7
  N25: U1.pin12, U1.pin32
  N26: U1.pin21, U7.pin7
  N27: U1.pin22, R19.Pin_0
  N28: U1.pin23, U7.pin5
  N29: U1.pin37, R13.Pin_1, U10.pin6
  N30: U1.pin38, R12.Pin_1, U10.pin5
  N31: U2.pin1, R2.Pin_0
  N32: U2.pin2, R1.Pin_0
  N33: U2.pin3, U6.pin5
  N34: U2.pin5, R32.Pin_1, U9.pin3
  N35: U2.pin6, U9.pin1
  N36: U2.pin9, U2.pin10, U11.pin1, U11.pin2, U11.pin3, U11.pin4, U11.pin7
  N37: U2.pin12, U2.pin32, R29.Pin_0, R30.Pin_0, R31.Pin_0, R27.Pin_1, R28.Pin_1, U9.pin8, U13.pin8
  N38: U2.pin17, R30.Pin_1, U13.pin6
  N39: U2.pin18, R31.Pin_1, U13.pin5
  N40: U2.pin23, R26.Pin_0
  N41: U2.pin37, R27.Pin_0, U11.pin6
  N42: U2.pin38, R28.Pin_0, U11.pin5
  N43: U5.pin1, U5.pin11
  N44: U5.pin3, R15.Pin_1
  N45: U5.pin4, R14.Pin_1
  N46: U5.pin7, R16.Pin_0
  N47: U5.pin15, R17.Pin_0
  N48: U5.pin17, R18.Pin_0
  N49: C1.pin1, U7.pin8
  N50: R26.Pin_1, R25.Pin_1, C2.pin1
  N51: R32.Pin_0, U9.pin4
  N52: R19.Pin_1, U7.pin6
  N53: R20.Pin_1, X6.pin1
  N54: U13.pin1, U13.pin2, U13.pin3, U13.pin4, U13.pin7
  N55: X4.pin2, X5.pin2

notes:
  Licensed under CERN OHL v.1.2
  1
  +
  GND
  +5V
  -
  2
  3
  +3.3V
  >
  greeneinvents.com
  6/28/2015
