# Fritzing sketch id1568_TR_FNL_with_gnd_plane_0 (saved by Fritzing 0.9.2b)
circuit board: 10.16cm x 7.62cm
breadboards: 1

parts:
  U1 = IC, DIP package, 20 pins [chip_label=IC]  # not connected
  U2 = IC, DIP package, 8 pins [chip_label=IC]
  U3 = IC, DIP package, 8 pins [chip_label=IC]
  Pad1 = Pad [width=20.8148591164733 height=3.79937208161887 connect=center]

nets:
  N1: U2.pin2, U2.pin3, U2.pin4
  N2: U3.pin2, U3.pin3, Pad1.pad

notes:
  1
  +
  greeneinvents.com
  Licenced under CERN OHL v.1.2
  JP3B
  6/27/2015
  3.3v
  GND
  5v
  12v
