# Fritzing sketch id1569_Untitled_Sketch_0 (saved by Fritzing 0.9.0b)
breadboards: 1

parts:
  U1 = 555 Timer [package="DIP8 [THT]"]
  R1 = Resistor [tolerance=±5% resistance=150 package=THT]
  R2 = Resistor [tolerance=±5% resistance=1.5k package=THT]
  C1 = Ceramic Capacitor [capacitance=0.01µF package="100 mil [THT, multilayer]"]
  R5 = Resistor [tolerance=±5% resistance=4.7 package=THT]
  R6 = Resistor [tolerance=±5% resistance=10k package=THT]
  R7 = Resistor [tolerance=±5% resistance=4.7k package=THT]
  R8 = Resistor [tolerance=±5% resistance=470k package=THT]
  R9 = Resistor [tolerance=±5% resistance=2.2k package=THT]
  R10 = Resistor [tolerance=±5% resistance=1k package=THT]
  R11 = Resistor [tolerance=±5% resistance=2.7k package=THT]
  R12 = Resistor [tolerance=±5% resistance=100k package=THT]
  R13 = Resistor [tolerance=±5% resistance=456 package=THT]
  C2 = Ceramic Capacitor [capacitance=0.1µF package="100 mil [THT, multilayer]"]
  C3 = Electrolytic Capacitor [capacitance=100µF voltage=16V package="100 mil [THT, electrolytic]"]
  C4 = Electrolytic Capacitor [capacitance=100µF voltage=16V package="100 mil [THT, electrolytic]"]
  C5 = Ceramic Capacitor [capacitance=0.01µF package="100 mil [THT, multilayer]"]
  C6 = Ceramic Capacitor [capacitance=47pF package="100 mil [THT, multilayer]"]
  C7 = Ceramic Capacitor [capacitance=0.1µF package="100 mil [THT, multilayer]"]
  C8 = Electrolytic Capacitor [capacitance=4.7µF voltage=16V package="100 mil [THT, electrolytic]"]
  C9 = Electrolytic Capacitor [capacitance=22µF voltage=16V package="100 mil [THT, electrolytic]"]
  C10 = Electrolytic Capacitor [capacitance=220µF voltage=16V package="100 mil [THT, electrolytic]"]
  Q1 = PNP-Transistor [part_number=SK100 package="TO92 [THT]"]
  Q2 = NPN-Transistor [part_number=BC549C package="TO92 [THT]"]
  Q3 = NPN-Transistor [part_number=BC549 package="TO92 [THT]"]
  Q4 = NPN-Transistor [part_number=BC549 package="TO92 [THT]"]
  S1 = Pushbutton [package=THT]
  Q5 = QRD1114 [part_number="H0-4R IR Sensor" package=qrd1114]
  VCC1 = Battery block 9V
  R4 = Resistor [tolerance=±5% resistance=47 package=THT]
  R3 = Resistor [tolerance=±5% resistance=47 package=THT]
  U2 = mystery part, 2 pins [chip_label="audio Jack"]

nets:
  N1: U1.Ground, U1.Reset, U1.Vcc_Supply_Voltage, R1.Pin_0, R10.Pin_1, R13.Pin_1, C3.+, C10.+, Q1.E, S1.leg0, VCC1.+, R3.Pin_0
  N2: U1.Trigger, U1.Threshold, R2.Pin_1, C1.1
  N3: U1.Output, R4.Pin_0
  N4: U1.Control_Voltage, C2.0
  N5: U1.Discharge, R1.Pin_1, R2.Pin_0
  N6: C1.0, R9.Pin_1, C2.1, C3.-, C4.-, C7.0, C10.-, Q2.E, Q3.E, S1.leg1, Q5.C, Q5.K, VCC1.-, U2.pin2
  N7: R5.Pin_0, Q1.C
  N8: R5.Pin_1, Q5.A
  N9: R6.Pin_0, C5.0, Q5.E
  N10: R6.Pin_1, R7.Pin_1, R10.Pin_0, R11.Pin_1, C4.+
  N11: R7.Pin_0, C6.0, Q2.C, Q4.B
  N12: R8.Pin_0, C5.1, C6.1, Q2.B
  N13: R8.Pin_1, R9.Pin_0, C7.1, Q4.E
  N14: R11.Pin_0, R12.Pin_0, C8.+, Q4.C
  N15: R12.Pin_1, R13.Pin_0, C9.+, Q3.C
  N16: C8.-, Q3.B
  N17: C9.-, U2.pin1
  N18: Q1.B, R4.Pin_1, R3.Pin_1
