# Fritzing sketch id156_555_timer_0 (saved by Fritzing 0.9.2b)
circuit board: 3.87057cm x 5.36593cm
breadboards: 1

parts:
  U1 = 555 Timer [package="DIP8 [THT]"]
  R1 = Resistor [tolerance=±5% resistance=220 package=THT]
  D1 = Zener Diode [part_number=1N4732A breakdown_voltage=3.6V package="300 mil [THT]"]
  C1 = Capacitor [package=cap-pth-5mm]
  R2 = Resistor [tolerance=±5% resistance=220 package=THT]
  LED1 = smd LED [color="Red (633nm)" package="0603 [SMD]"]
  C2 = Capacitor [package=cap-pth-5mm]
  R3 = Resistor [tolerance=±5% resistance=220 package=THT]
  U2 = Voltage Regulator - 5V [package="TO220 [THT]"]
  JP2 = Header 2 [package=molex-1x2_lock]

nets:
  N1: U1.Ground, C1.2, C2.2, R3.Pin_0, U2.GND, JP2.1
  N2: U1.Trigger, U1.Threshold, R1.Pin_0, D1.cathode, R2.Pin_1
  N3: U1.Output, LED1.anode
  N4: U1.Reset, U1.Vcc_Supply_Voltage, R2.Pin_0, U2.output_voltage
  N5: U1.Control_Voltage, C2.1
  N6: U1.Discharge, R1.Pin_1, D1.anode, C1.1
  N7: LED1.cathode, R3.Pin_1
  N8: U2.input_voltage, JP2.2
