# Fritzing sketch id1570_electroxylophone_0 (saved by Fritzing 0.9.2b)
breadboards: 2

parts:
  D1 = Rectifier Diode [part_number=1N4001 package="300 mil [THT]"]
  L1 = Solenoid
  Part1 = Arduino Uno (Rev3)
  R1 = Resistor [tolerance=±5% resistance=2.2k package=THT]
  L2 = Solenoid
  Q1 = npn-Powertransistor [package="TO220 [THT]"]
  Q2 = npn-Powertransistor [package="TO220 [THT]"]
  R2 = Resistor [tolerance=±5% resistance=2.2k package=THT]
  D2 = Rectifier Diode [part_number=1N4001 package="300 mil [THT]"]
  L3 = Solenoid
  Q3 = npn-Powertransistor [package="TO220 [THT]"]
  R3 = Resistor [tolerance=±5% resistance=2.2k package=THT]
  D3 = Rectifier Diode [part_number=1N4001 package="300 mil [THT]"]
  L4 = Solenoid
  Q4 = npn-Powertransistor [package="TO220 [THT]"]
  D4 = Rectifier Diode [part_number=1N4001 package="300 mil [THT]"]
  R4 = Resistor [tolerance=±5% resistance=2.2k package=THT]
  Q5 = npn-Powertransistor [package="TO220 [THT]"]
  D5 = Rectifier Diode [part_number=1N4001 package="300 mil [THT]"]
  R5 = Resistor [tolerance=±5% resistance=2.2k package=THT]
  L5 = Solenoid
  L6 = Solenoid
  Q6 = npn-Powertransistor [package="TO220 [THT]"]
  D6 = Rectifier Diode [part_number=1N4001 package="300 mil [THT]"]
  R6 = Resistor [tolerance=±5% resistance=2.2k package=THT]
  Q7 = npn-Powertransistor [package="TO220 [THT]"]
  R7 = Resistor [tolerance=±5% resistance=2.2k package=THT]
  D7 = Rectifier Diode [part_number=1N4001 package="300 mil [THT]"]
  L7 = Solenoid
  L8 = Solenoid
  Q8 = npn-Powertransistor [package="TO220 [THT]"]
  R8 = Resistor [tolerance=±5% resistance=2.2k package=THT]
  D8 = Rectifier Diode [part_number=1N4001 package="300 mil [THT]"]

nets:
  N1: D1.cathode, L1.pin2, L2.pin2, Q2.emitter, D2.cathode, L3.pin2, D3.cathode, L4.pin2, D4.cathode, D5.cathode, L5.pin2, L6.pin2, D6.cathode
  N2: D1.anode, L1.pin1, Q1.collector
  N3: Part1.D8, R1.Pin_1
  N4: Part1.D9_PWM, R7.Pin_1
  N5: Part1.D10_PWM/SS, R8.Pin_1
  N6: Part1.D3_PWM, R6.Pin_1
  N7: Part1.D4, R5.Pin_1
  N8: Part1.D5_PWM, R4.Pin_1
  N9: Part1.D6_PWM, R3.Pin_1
  N10: Part1.D7, R2.Pin_1
  N11: R1.Pin_0, Q1.base
  N12: L2.pin1, Q2.collector, D2.anode
  N13: Q1.emitter, Q3.emitter, Q4.emitter, Q5.emitter, Q6.emitter
  N14: Q2.base, R2.Pin_0
  N15: L3.pin1, Q3.collector, D3.anode
  N16: Q3.base, R3.Pin_0
  N17: L4.pin1, Q4.collector, D4.anode
  N18: Q4.base, R4.Pin_0
  N19: Q5.base, R5.Pin_0
  N20: Q5.collector, L5.pin1
  N21: L6.pin1, Q6.collector
  N22: Q6.base, R6.Pin_0
  N23: Q7.base, R7.Pin_0
  N24: Q7.collector, D7.anode, L7.pin1
  N25: Q7.emitter, Q8.emitter
  N26: D7.cathode, L7.pin2, L8.pin2, D8.cathode
  N27: L8.pin1, Q8.collector, D8.anode
  N28: Q8.base, R8.Pin_0
