# Fritzing sketch id1571_ecraft_la_0 (saved by Fritzing 0.9.2b)

parts:
  Part2 = gemma
  LED3 = Adafruit_FLORA_RGB_Smart_Pixel
  LED4 = Adafruit_FLORA_RGB_Smart_Pixel

nets:
  N1: Part2.connector2, LED3.connector2
  N2: Part2.connector18, LED3.connector3, LED4.connector3
  N3: Part2.connector70, LED3.connector1, LED4.connector1
  N4: LED3.connector4, LED4.connector2
