# Fritzing sketch id1572_Nokia5110DS1820_0 (saved by Fritzing 0.9.2b)
circuit board: 7cm x 5.6cm
breadboards: 1

parts:
  ARDUINO_NANO_R3 = Arduino Nano (Rev3.0) (ICSP)
  4_7k = Resistor [tolerance=±5% resistance=220 package=THT]
  PIEZO = Piezo Speaker
  Aussen = female pin header, 3 pins [form="♀ (female)"]
  Motor = female pin header, 3 pins [form="♀ (female)"]
  Akku = female pin header, 3 pins [form="♀ (female)"]
  NOKIA_5110_LCD = female pin header, 8 pins [form="♀ (female)"]
  12V = Power plug
  RGB-LED = RGB LED (com. cathode, rgb) [package="5 mm [THT]"]
  R1 = Resistor [tolerance=±5% resistance=220 package=THT]
  R2 = Resistor [tolerance=±5% resistance=220 package=THT]
  R3 = Resistor [tolerance=±5% resistance=220 package=THT]

nets:
  GND: ARDUINO_NANO_R3.GND, PIEZO.pin1, Aussen.pin3, Motor.pin3, Akku.pin3, NOKIA_5110_LCD.pin7, 12V.GND, RGB-LED.common_cathode
  N1: ARDUINO_NANO_R3.D3, R3.Pin_0
  N2: ARDUINO_NANO_R3.D4, PIEZO.pin2
  N3: ARDUINO_NANO_R3.D5, R2.Pin_0
  N4: ARDUINO_NANO_R3.D6, R1.Pin_0
  N5: ARDUINO_NANO_R3.D7, 4_7k.Pin_1, Aussen.pin2, Motor.pin2, Akku.pin2
  N6: ARDUINO_NANO_R3.D8, NOKIA_5110_LCD.pin2
  N7: ARDUINO_NANO_R3.D9, NOKIA_5110_LCD.pin3
  N8: ARDUINO_NANO_R3.D10, NOKIA_5110_LCD.pin4
  N9: ARDUINO_NANO_R3.D11/MOSI, NOKIA_5110_LCD.pin5
  N10: ARDUINO_NANO_R3.D12/MISO, NOKIA_5110_LCD.pin6
  VIN: ARDUINO_NANO_R3.VIN, 12V.VCC
  N11: ARDUINO_NANO_R3.5V, 4_7k.Pin_0, Aussen.pin1, Motor.pin1, Akku.pin1
  N12: ARDUINO_NANO_R3.3V3, NOKIA_5110_LCD.pin1, NOKIA_5110_LCD.pin8
  N13: RGB-LED.red_anode, R1.Pin_1
  N14: RGB-LED.green_anode, R2.Pin_1
  N15: RGB-LED.blue_anode, R3.Pin_1

notes:
  +
  +12V
  -
  data
  1-VCC
  2-GND
  3-SCE
  4-RST
  5-D/C
  6-MOSI
  7-SCLK
  8-LED
  GOVECS
  Temperaturdisplay
  Enrico Sadlowski  /  August 2015
  Rot
  Grün
  Blau
