# Fritzing sketch id1573_elevador1_0 (saved by Fritzing 0.9.0b)
breadboards: 1

parts:
  R1 = Resistor [tolerance=±5% resistance=330 package=THT]
  U1 = Optocoupler [package=THT]
  R2 = Resistor [tolerance=±5% resistance=330 package=THT]
  U2 = Optocoupler [package=THT]
  R3 = Resistor [tolerance=±5% resistance=330 package=THT]
  U3 = Optocoupler [package=THT]
  R4 = Resistor [tolerance=±5% resistance=330 package=THT]
  U4 = Optocoupler [package=THT]
  V1 = DC Power [voltage=12V]
  Parte1 = DB25F
  M1 = Stepper Motor - Unipolar
  IC1 = L293D [package=THT]

nets:
  N1: R1.Pin_0, Parte1.pin2
  N2: R1.Pin_1, U1.Pin_1
  GND: U1.Pin_2, U2.Pin_2, U3.Pin_2, U4.Pin_2, V1.V-, IC1.0V
  N3: U1.Pin_4, IC1.In_1
  5V: U1.Pin_6, U2.Pin_6, U3.Pin_6, U4.Pin_6, IC1.Enable_1, IC1.Enable_2, IC1.+V
  N4: R2.Pin_0, Parte1.pin3
  N5: R2.Pin_1, U2.Pin_1
  N6: U2.Pin_4, IC1.In_2
  N7: R3.Pin_0, Parte1.pin4
  N8: R3.Pin_1, U3.Pin_1
  N9: U3.Pin_4, IC1.In_3
  N10: R4.Pin_0, Parte1.pin5
  N11: R4.Pin_1, U4.Pin_1
  N12: U4.Pin_4, IC1.In_4
  N13: V1.V+, M1.COMMON_1, M1.COMMON_2, IC1.+Vmotor
  N14: M1.A, IC1.Out_4_(_Controlled_by_Enable_2_)
  N15: M1.C, IC1.Out_3_(_Controlled_by_Enable_2_)
  N16: M1.B, IC1.Out_1_(_Controlled_by_Enable_1_)
  N17: M1.D, IC1.Out_2_(_Controlled_by_Enable_1_)
