# Fritzing sketch id1574_aufzug_0 (saved by Fritzing 0.8.4b)
breadboards: 1

parts:
  R2 = Resistor [tolerance=±5% resistance=220 package=THT]
  R4 = Resistor [tolerance=±5% resistance=220 package=THT]
  R7 = Resistor [tolerance=±5% resistance=220 package=THT]
  R8 = Resistor [tolerance=±5% resistance=220 package=THT]
  R9 = Resistor [tolerance=±5% resistance=220 package=THT]
  R10 = Resistor [tolerance=±5% resistance=220 package=THT]
  R11 = Resistor [tolerance=±5% resistance=220 package=THT]
  R12 = Resistor [tolerance=±5% resistance=220 package=THT]
  R13 = Resistor [tolerance=±5% resistance=220 package=THT]
  R14 = Resistor [tolerance=±5% resistance=220 package=THT]
  R15 = Resistor [tolerance=±5% resistance=220 package=THT]
  LED5 = LED - 5mm [color="Green (555nm)" package="5 mm [THT]"]
  LED6 = LED - 5mm [color="Red (635nm)" package="5 mm [THT]"]
  LED7 = LED - 5mm [color="Yellow (585nm)" package="5 mm [THT]"]
  LED8 = LED - 5mm [color="Green (555nm)" package="5 mm [THT]"]
  LED9 = LED - 5mm [color="Red (635nm)" package="5 mm [THT]"]
  LED10 = LED - 5mm [color="Green (555nm)" package="5 mm [THT]"]
  LED11 = LED - 5mm [color="Yellow (585nm)" package="5 mm [THT]"]
  LED12 = LED - 5mm [color="Green (555nm)" package="5 mm [THT]"]
  LED13 = LED - 5mm [color="Green (555nm)" package="5 mm [THT]"]
  LED14 = LED - 5mm [color="Yellow (585nm)" package="5 mm [THT]"]
  LED15 = LED - 5mm [color="Yellow (585nm)" package="5 mm [THT]"]
  Bauteil1 = Arduino Uno (Rev3)
  R29 = Resistor [tolerance=±5% resistance=220 package=THT]
  LED17 = LED - 5mm [color="Yellow (585nm)" package="5 mm [THT]"]

nets:
  N1: R2.Pin_0, LED8.anode
  N2: R2.Pin_1, Bauteil1.D3_PWM
  N3: R4.Pin_0, LED5.anode
  N4: R4.Pin_1, Bauteil1.D2
  N5: R7.Pin_0, LED12.anode
  N6: R7.Pin_1, Bauteil1.D4
  N7: R8.Pin_0, LED13.anode
  N8: R8.Pin_1, Bauteil1.D5_PWM
  N9: R9.Pin_0, LED10.anode
  N10: R9.Pin_1, Bauteil1.D6_PWM
  N11: R10.Pin_0, LED15.anode
  N12: R10.Pin_1, Bauteil1.D13/SCK
  N13: R11.Pin_0, LED6.anode
  N14: R11.Pin_1, Bauteil1.D7
  N15: R12.Pin_0, LED9.anode
  N16: R12.Pin_1, Bauteil1.D8
  N17: R13.Pin_0, LED11.anode
  N18: R13.Pin_1, Bauteil1.D10_PWM/SS
  N19: R14.Pin_0, LED14.anode
  N20: R14.Pin_1, Bauteil1.D12/MISO
  N21: R15.Pin_0, LED7.anode
  N22: R15.Pin_1, Bauteil1.D11_PWM/MOSI
  N23: LED5.cathode, LED6.cathode, LED7.cathode, LED8.cathode, LED9.cathode, LED11.cathode, LED12.cathode, LED13.cathode, LED14.cathode, LED15.cathode, Bauteil1.GND, LED17.cathode
  N24: Bauteil1.D9_PWM, R29.Pin_1
  N25: R29.Pin_0, LED17.anode
