# Fritzing sketch id1575_embClusterArduino_0 (saved by Fritzing 0.9.3b)
circuit board: 5.90858cm x 6.8831cm
breadboards: 2

parts:
  R4 = Resistor [tolerance=±5% resistance=1k package="0603 [SMD]"]
  R5 = Resistor [tolerance=±5% resistance=1k package="0603 [SMD]"]
  R9 = Resistor [tolerance=±5% resistance=1k package="0603 [SMD]"]
  LED3 = smd LED [color="Red (633nm)" package="0603 [SMD]"]
  CHIP1-USB1 = USB connector [package=THT]
  USB2 = USB UART [package=ssop28db]
  C10 = Capacitor [package=0603-cap]
  C11 = Capacitor [package=0805]
  C12 = Capacitor [package=0603-cap]
  C13 = Capacitor [package=0603-cap]
  C14 = Capacitor [package=0603-cap]
  C15 = Capacitor [package=0603-cap]
  C16 = Capacitor [package=0603-cap]
  C17 = Capacitor [package=0805]
  C18 = Capacitor [package=0603-cap]
  R10 = Resistor [tolerance=±5% resistance=1k package="0603 [SMD]"]
  R11 = Resistor [tolerance=±5% resistance=0 package="1206 [SMD]"]
  R12 = Resistor [tolerance=±5% resistance=1k package="0603 [SMD]"]
  R13 = Resistor [tolerance=±5% resistance=1k package="0603 [SMD]"]
  R14 = Resistor [tolerance=±5% resistance=1k package="0603 [SMD]"]
  R15 = Resistor [tolerance=±5% resistance=1k package="0603 [SMD]"]
  LED4 = smd LED [color="Red (633nm)" package="0603 [SMD]"]
  LED5 = smd LED [color="Red (633nm)" package="0603 [SMD]"]
  XTAL2 = Crystal [frequency="20 MHz" package=THT]
  S2 = Pushbutton [package="[THT]"]
  J2 = AVR ISP 6 Pin [package=2x3]
  CHIP1-USB2 = USB connector [package=THT]
  U3 = ATmega328 [package=tqfp]
  USB3 = USB UART [package=ssop28db]
  C19 = Capacitor [package=0805]
  C20 = Capacitor [package=0603-cap]
  C21 = Capacitor [package=0603-cap]
  C22 = Capacitor [package=0603-cap]
  C23 = Capacitor [package=0603-cap]
  C24 = Capacitor [package=0805]
  C25 = Capacitor [package=0603-cap]
  C26 = Capacitor [package=0603-cap]
  C27 = Capacitor [package=0603-cap]
  R16 = Resistor [tolerance=±5% resistance=1k package="0603 [SMD]"]
  R17 = Resistor [tolerance=±5% resistance=1k package="0603 [SMD]"]
  R18 = Resistor [tolerance=±5% resistance=1k package="0603 [SMD]"]
  R19 = Resistor [tolerance=±5% resistance=0 package="1206 [SMD]"]
  R20 = Resistor [tolerance=±5% resistance=1k package="0603 [SMD]"]
  R21 = Resistor [tolerance=±5% resistance=1k package="0603 [SMD]"]
  LED6 = smd LED [color="Red (633nm)" package="0603 [SMD]"]
  LED7 = smd LED [color="Red (633nm)" package="0603 [SMD]"]
  XTAL3 = Crystal [frequency="20 MHz" package=THT]
  J3 = AVR ISP 6 Pin [package=2x3]
  S3 = Pushbutton [package="[THT]"]
  U2 = ATmega328 [package=tqfp]

nets:
  SCL: R4.Pin_0, U3.PC5(ADC5_SCL), U2.PC5(ADC5_SCL)
  5V: R4.Pin_1, R5.Pin_1, LED3.anode, USB2.VCCIO, USB2.VCC, C11.1, C13.1, C17.1, C18.1, R11.Pin_1, R15.Pin_1, LED4.anode, LED5.anode, J2.2, U3.VCC, U3.AVCC, USB3.VCCIO, USB3.VCC, C19.1, C23.1, C24.1, C26.1, R18.Pin_1, R19.Pin_1, LED6.anode, LED7.anode, J3.2, U2.VCC, U2.AVCC
  SDA: R5.Pin_0, U3.PC4(ADC4_SDA), U2.PC4(ADC4_SDA)
  N1: R9.Pin_0, LED3.cathode
  GND: R9.Pin_1, CHIP1-USB1.GND, CHIP1-USB1.chassis5, USB2.GND7, USB2.GND18, USB2.GND21, USB2.AGND, USB2.TEST, C10.2, C11.2, C12.2, C13.2, C14.2, C15.2, C17.2, C18.2, S2.Pin_1, S2.Pin_2, J2.6, CHIP1-USB2.GND, CHIP1-USB2.chassis6, U3.GND, U3.AGND, USB3.GND7, USB3.GND18, USB3.GND21, USB3.AGND, USB3.TEST, C19.2, C20.2, C21.2, C23.2, C24.2, C25.2, C26.2, C27.2, J3.6, S3.Pin_1, S3.Pin_2, U2.GND, U2.AGND
  N2: CHIP1-USB1.5V, R11.Pin_0
  N3: CHIP1-USB1.d-, USB2.USBDM
  N4: CHIP1-USB1.d+, USB2.USBDP
  N5: USB2.TXD, R13.Pin_1
  N6: USB2.DTR, C16.2
  N7: USB2.RXD, R12.Pin_1
  N8: USB2.3V3OUT, C14.1
  N9: USB2.RXLED, R10.Pin_1
  N10: USB2.TXLED, R14.Pin_1
  N11: C10.1, U2.AREF
  N12: C12.1, XTAL2.pin_0, U2.PB7(XTAL2_TOSC2)
  N13: C15.1, XTAL2.pin_1, U2.PB6(XTAL1_TOSC1)
  RESET2: C16.1, R15.Pin_0, S2.Pin_3, S2.Pin_4, J2.5, U2.PC6(_RESET)
  N14: R10.Pin_0, LED5.cathode
  N15: R12.Pin_0, U2.PD1(TXD)
  N16: R13.Pin_0, U2.PD0(RXD)
  N17: R14.Pin_0, LED4.cathode
  N18: J2.1, U2.PB4(MISO)
  N19: J2.3, U2.PB5(SCK)
  N20: J2.4, U2.PB3(MOSI_OC2)
  N21: CHIP1-USB2.5V, R19.Pin_0
  N22: CHIP1-USB2.d-, USB3.USBDM
  N23: CHIP1-USB2.d+, USB3.USBDP
  N24: U3.PB6(XTAL1_TOSC1), C25.1, XTAL3.pin_1
  N25: U3.PB7(XTAL2_TOSC2), C20.1, XTAL3.pin_0
  N26: U3.PB3(MOSI_OC2), J3.4
  N27: U3.PB4(MISO), J3.1
  N28: U3.PB5(SCK), J3.3
  N29: U3.AREF, C21.1
  RESET1: U3.PC6(_RESET), C22.1, R18.Pin_0, J3.5, S3.Pin_3, S3.Pin_4
  N30: U3.PD0(RXD), R17.Pin_0
  N31: U3.PD1(TXD), R21.Pin_0
  N32: USB3.TXD, R17.Pin_1
  N33: USB3.DTR, C22.2
  N34: USB3.RXD, R21.Pin_1
  N35: USB3.3V3OUT, C27.1
  N36: USB3.RXLED, R20.Pin_1
  N37: USB3.TXLED, R16.Pin_1
  N38: R16.Pin_0, LED7.cathode
  N39: R20.Pin_0, LED6.cathode
