# Fritzing sketch id1576_EMD_0 (saved by Fritzing 0.9.2b)
breadboards: 2

parts:
  Part1 = Arduino Ethernet Shield (Rev3)
  U1 = MAX6675 [package=so08]
  U2 = POT [package=pot_alpha_rv16af-20]
  VCC1 = Battery block 9V
  M1 = DC Motor
  U3 = LCD-16X2 [package=lcd-16x2_noholes]
  LED1 = DUO LED RG [package="5 mm [THT]"]
  LED2 = DUO LED RG [package="5 mm [THT]"]
  R1 = Resistor [tolerance=±5% resistance=220 package="0805 [SMD]"]
  R2 = Resistor [tolerance=±5% resistance=220 package="0402 [SMD]"]
  Q1 = TRANSISTOR_PNP [package=to-92]
  R3 = Resistor [tolerance=±5% resistance=220 package="1206 [SMD]"]
  U4 = BUTTONPAD-4X4 [package=buttonpad-4x4]  # not connected
  S1 = Toggle Switch [package=THT]
  S2 = Toggle Switch [package=THT]
  M2 = DC Motor

nets:
  GND: Part1.GND, U2.E, VCC1.-, U3.VSS, LED1.common_cathode, LED2.common_cathode, Q1.C, M2.pin_1
  N1: Part1.SPI/D12, R2.Pin_0
  N2: Part1.SPI/D13, U1.VDD
  N3: Part1.A0, U2.S
  N4: Part1.A4/SDA, U3.VO
  N5: Part1.A5/SCL, U3.RS
  N6: Part1.TX/D1, U1.T+
  N7: Part1.D2, R3.Pin_0
  N8: Part1.SDCS, R1.Pin_0
  N9: Part1.PWM_D6, U1.T-
  N10: Part1.D7, S2.L1
  5V: Part1.5V, U1.VSS
  N11: Part1.IOREF, S1.COM
  N12: U1.SCK, VCC1.+, M1.pin_2, M2.pin_2
  N13: U2.A, S2.COM
  N14: M1.pin_1, Q1.E
  N15: U3.VDD, S1.L1
  N16: LED1.green_anode, R1.Pin_1
  N17: LED2.red_anode, R2.Pin_1
  N18: Q1.B, R3.Pin_1
