# Fritzing sketch id1577_emenda_rapida_0 (saved by Fritzing 0.9.0b)
circuit board: 6cm x 5cm
breadboards: 1

parts:
  Garagino_Rev_1 = arduino.fzp
  J1 = Screw terminal - 2 pins [package=THT]
  J2 = Screw terminal - 2 pins [package=THT]
  J3 = Screw terminal - 2 pins [package=THT]
  J4 = Screw terminal - 2 pins [package=THT]
  J5 = Screw terminal - 2 pins [package=THT]
  J6 = Screw terminal - 2 pins [package=THT]
  J7 = Screw terminal - 2 pins [package=THT]
  J9 = Screw terminal - 2 pins [package=THT]
  J11 = Screw terminal - 2 pins [package=THT]
  J12 = Screw terminal - 2 pins [package=THT]
  J13 = Screw terminal - 2 pins [package=THT]
  J14 = Screw terminal - 2 pins [package=THT]
  J15 = Screw terminal - 2 pins [package=THT]
  J10 = Screw terminal - 2 pins [package=THT]

nets:
  N1: Garagino_Rev_1.connector0, J4.pin2
  N2: Garagino_Rev_1.connector1, J12.pin1
  N3: Garagino_Rev_1.connector2, J5.pin2
  N4: Garagino_Rev_1.connector3, J7.pin1
  N5: Garagino_Rev_1.connector4, J7.pin2
  N6: Garagino_Rev_1.connector5, J6.pin1
  N7: Garagino_Rev_1.connector6, J6.pin2
  N8: Garagino_Rev_1.connector7, J10.pin1
  N9: Garagino_Rev_1.connector8, J10.pin2
  N10: Garagino_Rev_1.connector9, J9.pin1
  N11: Garagino_Rev_1.connector10, J9.pin2
  N12: Garagino_Rev_1.connector11, J13.pin1
  N13: Garagino_Rev_1.connector12, J13.pin2
  N14: Garagino_Rev_1.connector13, J14.pin1
  N15: Garagino_Rev_1.connector14, J14.pin2
  N16: Garagino_Rev_1.connector15, J15.pin1
  N17: Garagino_Rev_1.connector16, J15.pin2
  N18: Garagino_Rev_1.connector17, J11.pin2
  N19: Garagino_Rev_1.connector18, J5.pin1
  N20: Garagino_Rev_1.connector19, J4.pin1
  N21: Garagino_Rev_1.connector21, J12.pin2
  N22: Garagino_Rev_1.connector22, J3.pin2
  N23: Garagino_Rev_1.connector23, J3.pin1
  N24: Garagino_Rev_1.connector24, J2.pin2
  N25: Garagino_Rev_1.connector25, J2.pin1
  N26: Garagino_Rev_1.connector26, J1.pin2
  N27: Garagino_Rev_1.connector27, J1.pin1
  N28: Garagino_Rev_1.connector28, J11.pin1
