# Fritzing sketch id1579_EMG_esquematic_v3_0 (saved by Fritzing 0.9.2b)
breadboards: 1

parts:
  U1 = OP37 - Low Noise, Precision, High Speed Op Amp [part_number=LM741]
  INA = AD8226 - Rail-to-Rail output Instrumentation Amplifier [part_number="INA 126P"]
  R10 = Resistor [tolerance=±5% resistance=220 package="0603 [SMD]"]
  U3 = OP37 - Low Noise, Precision, High Speed Op Amp [part_number=LM741]
  C1 = Electrolytic Capacitor [capacitance=10μF package="0605 [SMD, electrolytic]"]
  R5 = Resistor [tolerance=±5% resistance=10k package="0603 [SMD]"]
  R2 = Resistor [tolerance=±5% resistance=10k package="0603 [SMD]"]
  U2 = OP37 - Low Noise, Precision, High Speed Op Amp [part_number=LM741]
  R6 = Resistor [tolerance=±5% resistance=10k package="0603 [SMD]"]
  R3 = Resistor [tolerance=±5% resistance=16k package="0603 [SMD]"]
  R4 = Resistor [tolerance=±5% resistance=46.7k package="0603 [SMD]"]
  R7 = Resistor [tolerance=±5% resistance=10k package="0603 [SMD]"]
  Atmega_328 = Arduino Leonardo (Rev3b)
  R1 = Resistor [tolerance=±5% resistance=10k package="0402 [SMD]"]
  R9 = Resistor [tolerance=±5% resistance=1M package="0805 [SMD]"]
  R4_2 = Resistor [tolerance=±5% resistance=330k package="0805 [SMD]"]
  R10_2 = Resistor [tolerance=±5% resistance=1M package="1206 [SMD]"]

nets:
  N1: U1.-IN, R2.Pin_0, R1.Pin_1
  N2: U1.+IN, R4.Pin_1
  -9V: U1.-V, INA.-VS, U3.-V, U2.-V, R3.Pin_0
  N3: U1.OUT, R5.Pin_0, R2.Pin_1
  9V: U1.V+, INA.+VS, U3.V+, U2.V+
  Pad (-): INA.-IN, R4_2.Pin_0, R10_2.Pin_0
  N4: INA.RG#2, R10.Pin_1
  N5: INA.RG#3, R10.Pin_0
  Pad (+): INA.+IN, R9.Pin_1
  GND/REF - Ground: INA.REF, U3.+IN, C1.-, Atmega_328.GND, R9.Pin_0
  N6: INA.VOUT, C1.+
  N7: U3.-IN, R5.Pin_1, R7.Pin_0
  N8: U3.OUT, R7.Pin_1, Atmega_328.A0
  N9: U2.-IN, U2.OUT, R6.Pin_1
  N10: U2.+IN, R3.Pin_1, R4.Pin_0
  Serial Comunication: Atmega_328.D0/RX
  Serial comunication: Atmega_328.D1/TX
  5V: Atmega_328.5V
  Sincronismo - Spare: Atmega_328.D13_PWM
