# Fritzing sketch id1580_EmonTX_Due_0 (saved by Fritzing 0.9.2b)
circuit board: 10.2cm x 5.35cm
breadboards: 1

parts:
  RFM12B = RFM12b HopeRF Transceiver
  C1 = Ceramic Capacitor [capacitance=100nF package="100 mil [THT, multilayer]"]
  R1 = Resistor [tolerance=±5% resistance=10k package=THT]
  ANT = Antenna
  TRS1 = Audio Jack (TRS) 3.5mm [package="4Ucon 08780 [THT]"]
  C2 = Electrolytic Capacitor [capacitance=10µF package="100 mil [THT, electrolytic]"]
  R2 = Resistor [tolerance=±5% resistance=6.8k package=THT]
  R3 = Resistor [tolerance=±5% resistance=100k package=THT]
  R5 = Resistor [tolerance=±5% resistance=100k package=THT]
  TRS2 = Audio Jack (TRS) 3.5mm [package="4Ucon 08780 [THT]"]
  C3 = Electrolytic Capacitor [capacitance=10µF package="100 mil [THT, electrolytic]"]
  R7 = Resistor [tolerance=±5% resistance=100k package=THT]
  R8 = Resistor [tolerance=±5% resistance=100k package=THT]
  R9 = Resistor [tolerance=±5% resistance=100k package=THT]
  R10 = Resistor [tolerance=±5% resistance=100k package=THT]
  TRS3 = Audio Jack (TRS) 3.5mm [package="4Ucon 08780 [THT]"]
  C4 = Electrolytic Capacitor [capacitance=10µF package="100 mil [THT, electrolytic]"]
  R13 = Resistor [tolerance=±5% resistance=100k package=THT]
  R14 = Resistor [tolerance=±5% resistance=100k package=THT]
  R15 = Resistor [tolerance=±5% resistance=100k package=THT]
  R17 = Resistor [tolerance=±5% resistance=100k package=THT]
  TRS4 = Audio Jack (TRS) 3.5mm [package="4Ucon 08780 [THT]"]
  TRS5 = Audio Jack (TRS) 3.5mm [package="4Ucon 08780 [THT]"]
  C5 = Electrolytic Capacitor [capacitance=10µF package="100 mil [THT, electrolytic]"]
  C6 = Electrolytic Capacitor [capacitance=10µF package="100 mil [THT, electrolytic]"]
  R19 = Resistor [tolerance=±5% resistance=100k package=THT]
  R20 = Resistor [tolerance=±5% resistance=100k package=THT]
  R21 = Resistor [tolerance=±5% resistance=100k package=THT]
  R23 = Resistor [tolerance=±5% resistance=100k package=THT]
  TRS6 = Audio Jack (TRS) 3.5mm [package="4Ucon 08780 [THT]"]
  TRS7 = Audio Jack (TRS) 3.5mm [package="4Ucon 08780 [THT]"]
  C7 = Electrolytic Capacitor [capacitance=10µF package="100 mil [THT, electrolytic]"]
  C8 = Electrolytic Capacitor [capacitance=10µF package="100 mil [THT, electrolytic]"]
  R26 = Resistor [tolerance=±5% resistance=100k package=THT]
  R27 = Resistor [tolerance=±5% resistance=100k package=THT]
  R28 = Resistor [tolerance=±5% resistance=100k package=THT]
  R29 = Resistor [tolerance=±5% resistance=100k package=THT]
  R31 = Resistor [tolerance=±5% resistance=100k package=THT]
  R33 = Resistor [tolerance=±5% resistance=100k package=THT]
  R34 = Resistor [tolerance=±5% resistance=100k package=THT]
  R36 = Resistor [tolerance=±5% resistance=100k package=THT]
  R37 = Resistor [tolerance=±5% resistance=100k package=THT]
  R38 = Resistor [tolerance=±5% resistance=100k package=THT]
  TRS8 = Audio Jack (TRS) 3.5mm [package="4Ucon 08780 [THT]"]
  TRS9 = Audio Jack (TRS) 3.5mm [package="4Ucon 08780 [THT]"]
  TRS10 = Audio Jack (TRS) 3.5mm [package="4Ucon 08780 [THT]"]
  TRS11 = Audio Jack (TRS) 3.5mm [package="4Ucon 08780 [THT]"]
  TRS12 = Audio Jack (TRS) 3.5mm [package="4Ucon 08780 [THT]"]
  C9 = Electrolytic Capacitor [capacitance=10µF package="100 mil [THT, electrolytic]"]
  C10 = Electrolytic Capacitor [capacitance=10µF package="100 mil [THT, electrolytic]"]
  C11 = Electrolytic Capacitor [capacitance=10µF package="100 mil [THT, electrolytic]"]
  C12 = Electrolytic Capacitor [capacitance=10µF package="100 mil [THT, electrolytic]"]
  C13 = Electrolytic Capacitor [capacitance=10µF package="100 mil [THT, electrolytic]"]
  ARDUINO_DUE = Arduino Due (Rev2b)
  SPI = double row female pin header, 6 pins [form="♀ (female)"]
  R30 = Resistor [tolerance=±5% resistance=22 package=THT]
  R32 = Resistor [tolerance=±5% resistance=22 package=THT]
  R35 = Resistor [tolerance=±5% resistance=22 package=THT]
  R22 = Resistor [tolerance=±5% resistance=22 package=THT]
  R18 = Resistor [tolerance=±5% resistance=22 package=THT]
  R16 = Resistor [tolerance=±5% resistance=22 package=THT]
  R12 = Resistor [tolerance=±5% resistance=22 package=THT]
  R11 = Resistor [tolerance=±5% resistance=22 package=THT]
  R25 = Resistor [tolerance=±5% resistance=22 package=THT]
  R6 = Resistor [tolerance=±5% resistance=22 package=THT]
  R24 = Resistor [tolerance=±5% resistance=22 package=THT]
  R4 = Resistor [tolerance=±5% resistance=100k package=THT]

nets:
  MISO: RFM12B.1_SDO, SPI.pin1
  nIRQ: RFM12B.2_nIRQ, ARDUINO_DUE.D8_PWM
  N1: RFM12B.3_FSK/DATA, R1.Pin_1
  GND: RFM12B.7_GND, RFM12B.10_GND, C1.0, C2.-, R5.Pin_1, C3.-, R8.Pin_1, R10.Pin_1, C4.-, R13.Pin_1, R14.Pin_1, C5.-, C6.-, R19.Pin_1, R20.Pin_1, C7.-, C8.-, R27.Pin_1, R28.Pin_1, R29.Pin_1, R33.Pin_1, R38.Pin_1, C9.-, C10.-, C11.-, C12.-, C13.-, ARDUINO_DUE.GND, SPI.pin4
  N2: RFM12B.8_ANT, ANT.antenna_lead
  N3: RFM12B.9_VDD, C1.1
  MOSI: RFM12B.12_SDI, SPI.pin5
  SCLK: RFM12B.13_SCK, SPI.pin2
  SS: RFM12B.14_nSEL, ARDUINO_DUE.D10_PWM/SS0
  3.3V: R1.Pin_0, R7.Pin_0, R9.Pin_0, R15.Pin_0, R17.Pin_0, R21.Pin_0, R23.Pin_0, R26.Pin_0, R31.Pin_0, R34.Pin_0, R36.Pin_0, R37.Pin_0, ARDUINO_DUE.IOREF, R4.Pin_0
  N4: TRS1.Sleeve, C2.+, R2.Pin_1, R5.Pin_0, R4.Pin_1
  N5: TRS1.Ring, TRS1.Tip, R3.Pin_1
  A11: R2.Pin_0, R3.Pin_0, ARDUINO_DUE.A11
  N6: TRS2.Sleeve, C3.+, R7.Pin_1, R8.Pin_0, R6.Pin_1
  A0: TRS2.Ring, TRS2.Tip, ARDUINO_DUE.A0, R6.Pin_0
  N7: R9.Pin_1, R10.Pin_0, TRS3.Sleeve, C4.+, R11.Pin_1
  A1: TRS3.Ring, TRS3.Tip, ARDUINO_DUE.A1, R11.Pin_0
  N8: R13.Pin_0, R17.Pin_1, TRS4.Sleeve, C6.+, R12.Pin_1
  N9: R14.Pin_0, R15.Pin_1, TRS5.Sleeve, C5.+, R16.Pin_1
  A2: TRS4.Ring, TRS4.Tip, ARDUINO_DUE.A2, R12.Pin_0
  A3: TRS5.Ring, TRS5.Tip, ARDUINO_DUE.A3, R16.Pin_0
  N10: R19.Pin_0, R23.Pin_1, TRS6.Sleeve, C8.+, R18.Pin_1
  N11: R20.Pin_0, R21.Pin_1, TRS7.Sleeve, C7.+, R22.Pin_1
  A4: TRS6.Ring, TRS6.Tip, ARDUINO_DUE.A4, R18.Pin_0
  A10: TRS7.Ring, TRS7.Tip, ARDUINO_DUE.A10, R22.Pin_0
  N12: R26.Pin_1, R29.Pin_0, TRS12.Sleeve, C11.+, R24.Pin_1
  N13: R27.Pin_0, R36.Pin_1, TRS9.Sleeve, C9.+, R32.Pin_1
  N14: R28.Pin_0, R37.Pin_1, TRS10.Sleeve, C10.+, R30.Pin_1
  N15: R31.Pin_1, R38.Pin_0, TRS11.Sleeve, C13.+, R25.Pin_1
  N16: R33.Pin_0, R34.Pin_1, TRS8.Sleeve, C12.+, R35.Pin_1
  A9: TRS8.Ring, TRS8.Tip, ARDUINO_DUE.A9, R35.Pin_0
  A8: TRS9.Ring, TRS9.Tip, ARDUINO_DUE.A8, R32.Pin_0
  A7: TRS10.Ring, TRS10.Tip, ARDUINO_DUE.A7, R30.Pin_0
  A6: TRS11.Ring, TRS11.Tip, ARDUINO_DUE.A6, R25.Pin_0
  A5: TRS12.Ring, TRS12.Tip, ARDUINO_DUE.A5, R24.Pin_0

notes:
  Current Probe Inputs
  AC-AC Voltage Adapter Input
