# Fritzing sketch id1581_EMF_Detector_0 (saved by Fritzing 0.8.7b)
circuit board: 8.46667cm x 5.64444cm

parts:
  Netduino1 = Netduino
  ANT1 = Antenna
  R1 = Resistor [tolerance=±5% resistance=220 package=THT]
  LED1 = LED - 5mm [color="Blue (430nm)" package="5 mm [THT]"]

nets:
  N1: Netduino1.GND, R1.Pin_0
  N2: Netduino1.D10_PWM3, LED1.anode
  N3: Netduino1.A0, ANT1.antenna_lead
  N4: R1.Pin_1, LED1.cathode

notes:
  erik medeossi
