# Fritzing sketch id1582_Arduino_con_due_TLC_0 (saved by Fritzing 0.7.12b)
breadboards: 1

parts:
  TCL5940NT = IC, DIP package, 28 pins [chip_label=IC part_number=TLC5940NT]
  TCL5940NT1 = IC, DIP package, 28 pins [chip_label=IC part_number=TLC5940NT]
  LED1 = LED - 5mm [color="Green (555nm)" package="5 mm [THT]"]
  LED2 = LED - 5mm [color="Green (555nm)" package="5 mm [THT]"]
  LED3 = LED - 5mm [color="Green (555nm)" package="5 mm [THT]"]
  LED4 = LED - 5mm [color="Green (555nm)" package="5 mm [THT]"]
  LED5 = LED - 5mm [color="Green (555nm)" package="5 mm [THT]"]
  LED6 = LED - 5mm [color="Green (555nm)" package="5 mm [THT]"]
  LED7 = LED - 5mm [color="Green (555nm)" package="5 mm [THT]"]
  LED8 = LED - 5mm [color="Green (555nm)" package="5 mm [THT]"]
  LED9 = LED - 5mm [color="Green (555nm)" package="5 mm [THT]"]
  LED10 = LED - 5mm [color="Green (555nm)" package="5 mm [THT]"]
  LED11 = LED - 5mm [color="Green (555nm)" package="5 mm [THT]"]
  LED12 = LED - 5mm [color="Green (555nm)" package="5 mm [THT]"]
  LED13 = LED - 5mm [color="Green (555nm)" package="5 mm [THT]"]
  LED14 = LED - 5mm [color="Green (555nm)" package="5 mm [THT]"]
  LED15 = LED - 5mm [color="Green (555nm)" package="5 mm [THT]"]
  LED16 = LED - 5mm [color="Green (555nm)" package="5 mm [THT]"]
  LED17 = LED - 5mm [color="Green (555nm)" package="5 mm [THT]"]
  LED18 = LED - 5mm [color="Green (555nm)" package="5 mm [THT]"]
  LED19 = LED - 5mm [color="Green (555nm)" package="5 mm [THT]"]
  LED20 = LED - 5mm [color="Green (555nm)" package="5 mm [THT]"]
  LED21 = LED - 5mm [color="Green (555nm)" package="5 mm [THT]"]
  LED22 = LED - 5mm [color="Green (555nm)" package="5 mm [THT]"]
  LED23 = LED - 5mm [color="Green (555nm)" package="5 mm [THT]"]
  LED24 = LED - 5mm [color="Green (555nm)" package="5 mm [THT]"]
  LED25 = LED - 5mm [color="Green (555nm)" package="5 mm [THT]"]
  LED26 = LED - 5mm [color="Green (555nm)" package="5 mm [THT]"]
  LED27 = LED - 5mm [color="Green (555nm)" package="5 mm [THT]"]
  LED28 = LED - 5mm [color="Green (555nm)" package="5 mm [THT]"]
  LED29 = LED - 5mm [color="Green (555nm)" package="5 mm [THT]"]
  LED30 = LED - 5mm [color="Green (555nm)" package="5 mm [THT]"]
  LED31 = LED - 5mm [color="Green (555nm)" package="5 mm [THT]"]
  Pull_Up = Resistor [tolerance=±5% resistance=10k package=THT]
  Arduino1 = Arduino

nets:
  N1: TCL5940NT.pin1, LED2.anode
  N2: TCL5940NT.pin2, LED3.anode
  N3: TCL5940NT.pin3, LED4.anode
  N4: TCL5940NT.pin4, LED5.anode
  N5: TCL5940NT.pin5, LED6.anode
  N6: TCL5940NT.pin6, LED7.anode
  N7: TCL5940NT.pin7, LED8.anode
  N8: TCL5940NT.pin8, LED9.anode
  N9: TCL5940NT.pin9, LED10.anode
  N10: TCL5940NT.pin10, LED11.anode
  N11: TCL5940NT.pin11, LED12.anode
  N12: TCL5940NT.pin12, LED13.anode
  N13: TCL5940NT.pin13, LED14.anode
  N14: TCL5940NT.pin14, LED15.anode
  N15: TCL5940NT.pin15, LED16.anode
  N16: TCL5940NT.pin17, TCL5940NT1.pin25
  N17: TCL5940NT.pin18, Arduino1.D3
  N18: TCL5940NT.pin19, TCL5940NT.pin21, TCL5940NT1.pin19, TCL5940NT1.pin21, Pull_Up.Pin_1, Arduino1.+5V
  N19: TCL5940NT.pin20, TCL5940NT.pin22, TCL5940NT.pin27, TCL5940NT1.pin20, TCL5940NT1.pin22, TCL5940NT1.pin27, Arduino1.GND
  N20: TCL5940NT.pin23, Pull_Up.Pin_0, Arduino1.D10
  N21: TCL5940NT.pin24, Arduino1.D9
  N22: TCL5940NT.pin25, Arduino1.D11
  N23: TCL5940NT.pin26, Arduino1.D13
  N24: TCL5940NT.pin28, LED1.anode
  N25: TCL5940NT1.pin1, LED18.anode
  N26: TCL5940NT1.pin2, LED19.anode
  N27: TCL5940NT1.pin3, LED20.anode
  N28: TCL5940NT1.pin4, LED21.anode
  N29: TCL5940NT1.pin5, LED22.anode
  N30: TCL5940NT1.pin6, LED23.anode
  N31: TCL5940NT1.pin8, LED24.anode
  N32: TCL5940NT1.pin9, LED25.anode
  N33: TCL5940NT1.pin10, LED26.anode
  N34: TCL5940NT1.pin11, LED27.anode
  N35: TCL5940NT1.pin12, LED28.anode
  N36: TCL5940NT1.pin13, LED29.anode
  N37: TCL5940NT1.pin14, LED30.anode
  N38: TCL5940NT1.pin15, LED31.anode
  N39: TCL5940NT1.pin28, LED17.anode
  N40: LED1.cathode, LED2.cathode, LED3.cathode, LED4.cathode, LED5.cathode, LED6.cathode, LED7.cathode, LED8.cathode, LED9.cathode, LED10.cathode, LED11.cathode, LED12.cathode, LED13.cathode, LED14.cathode, LED15.cathode, LED16.cathode, LED17.cathode, LED18.cathode, LED19.cathode, LED20.cathode, LED21.cathode, LED22.cathode, LED23.cathode, LED24.cathode, LED25.cathode, LED26.cathode, LED27.cathode, LED28.cathode, LED29.cathode, LED30.cathode, LED31.cathode, Arduino1.3V3
