# Fritzing sketch id1586_LED_Encendido_Apagado_0 (saved by Fritzing 0.9.3b)
breadboards: 1

parts:
  Componente1 = Arduino Uno (Rev3)
  R1 = Resistor [tolerance=±5% resistance=330 package=THT]
  R2 = Resistor [tolerance=±5% resistance=10k package=THT]
  LED1 = LED - 5mm [color="Red (633nm)" package="5 mm [THT]"]
  S1 = Pushbutton [package="[THT]"]

nets:
  N1: Componente1.D8, Componente1.5V, R2.Pin_1, S1.Pin_3, S1.Pin_4
  N2: Componente1.D4, LED1.anode
  N3: Componente1.GND, R1.Pin_0, R2.Pin_0
  N4: R1.Pin_1, LED1.cathode
  N5: S1.Pin_1, S1.Pin_2
