# Fritzing sketch id1588_Robot_Schematic_0 (saved by Fritzing 0.9.2b)
breadboards: 1

parts:
  Back_Left = DC Motor
  Front_Right = DC Motor
  Back_Left_2 = DC Motor
  Front_Left = DC Motor
  Fan = DC Motor
  Infrared_Flame_Sensor = Infrared Proximity Sensor
  12_Volt_Battery = Battery block 9V
  Switch = SWITCH-MOMENTARY-2 [package=reed_switch_plastic]
  RF_transmitter = RF_RX
  Romeo1 = Romeo

nets:
  N1: Back_Left.pin_1, Front_Right.pin_1, Romeo1.connector37
  N2: Back_Left.pin_2, Front_Right.pin_2, Romeo1.connector38
  N3: Back_Left_2.pin_1, Front_Left.pin_1, Romeo1.connector39
  N4: Back_Left_2.pin_2, Front_Left.pin_2, Romeo1.connector40
  N5: Fan.pin_1, Romeo1.connector27
  N6: Fan.pin_2, Infrared_Flame_Sensor.GND, RF_transmitter.connector1, Romeo1.connector5
  N7: Infrared_Flame_Sensor.Vout, Romeo1.connector8
  N8: Infrared_Flame_Sensor.Vcc, RF_transmitter.connector4, Romeo1.connector4
  N9: 12_Volt_Battery.-, Romeo1.connector42
  N10: 12_Volt_Battery.+, Switch.2
  N11: Switch.1, Romeo1.connector41
  N12: RF_transmitter.connector2, Romeo1.connector19
  N13: RF_transmitter.connector3, Romeo1.connector18
