# Fritzing sketch id1589_robotic_arm_0 (saved by Fritzing 0.9.2b)
breadboards: 1

parts:
  Part1 = Arduino Leonardo (Rev3b)
  S2 = SWITCH-MOMENTARY-2 [package=tactile-pth-12mm]
  S3 = SWITCH-MOMENTARY-2 [package=tactile-pth-12mm]
  R2 = Resistor [tolerance=±5% resistance=220 package=THT]
  J1 = Basic Servo
  J2 = Basic Servo
  J3 = Basic Servo
  R3 = Resistor [tolerance=±5% resistance=220 package=THT]
  JOY1 = Adafruit_Arcade_Joystick

nets:
  N1: Part1.D1/TX, JOY1.connector5
  N2: Part1.D2/SDA, JOY1.connector4
  N3: Part1.D3_PWM/SCL, JOY1.connector3
  N4: Part1.D4/A6, JOY1.connector2
  N5: Part1.D6_PWM/A7, J2.pulse
  VCC: Part1.5V, J1.vcc, J2.vcc, J3.vcc
  N6: Part1.D12/A11, S3.1, R3.Pin_1
  N7: Part1.D13_PWM, J3.pulse
  GND: Part1.GND, R2.Pin_0, J1.gnd, J2.gnd, J3.gnd, R3.Pin_0
  N8: S2.1, R2.Pin_1

notes:
  2 buttons
  3 servos, 2 for arm movements, 1 for gripper close and open movement
  Joystick - control the arm movement
  Arduino Leonardo - microcontrooler to control the whole robotic arm
  resistor
  Breadboard
