# Fritzing sketch id158_555_Variable_Buzzer_0 (saved by Fritzing 0.7.4b)
breadboards: 1

parts:
  R1 = Rotary Potentiometer (Small) [maximum_resistance=500kΩ]
  C1 = Electrolytic Capacitor [capacitance=3.3µF voltage=50V package="100 mil [THT, electrolytic]"]
  VCC1 = 4 x AAA Battery Mount
  U1 = 555 Timer [package="DIP8 [THT]"]
  S1 = Round Pushbutton
  SPKR1 = Loudspeaker
  SPKR2 = Loudspeaker
  SPKR3 = Loudspeaker

nets:
  N1: R1.leg1, R1.wiper, VCC1.+, U1.Output, U1.Reset, U1.Vcc_Supply_Voltage, SPKR1.pin1, SPKR1.pin2, SPKR2.pin1, SPKR2.pin2, SPKR3.pin1, SPKR3.pin2
  N2: R1.leg2, C1.-, U1.Discharge, S1.leg0
  N3: C1.+, VCC1.-, U1.Ground
  N4: U1.Trigger, U1.Threshold, S1.leg1
