# Fritzing sketch id1593_Entradas_digitales_con_un_LED_0 (saved by Fritzing 0.7.10b)
breadboards: 1

parts:
  Arduino1 = Arduino
  S1 = Pushbutton [package="[THT]"]
  S2 = Pushbutton [package="[THT]"]
  R1 = Resistor [tolerance=±5% resistance=220 package=THT]
  LED1 = LED - 5mm [color="Red (633nm)" package="5 mm [THT]"]

nets:
  N1: Arduino1.D9, S1.Pin_1, S1.Pin_2
  N2: Arduino1.D8, S2.Pin_1, S2.Pin_2
  N3: Arduino1.D5, R1.Pin_1
  N4: Arduino1.GND, S1.Pin_3, S1.Pin_4, S2.Pin_3, S2.Pin_4, LED1.cathode
  N5: R1.Pin_0, LED1.anode

notes:
  Entradas digitales con un LED
  Jing Dai
