# Fritzing sketch id1594_ep2_0 (saved by Fritzing 0.9.3b)
breadboards: 1

parts:
  Componente1 = Arduino Mega 2560 (Rev3)
  U1 = QRE1113 [package=qre1113]  # not connected
  LED1 = LED - 5mm [color="Red (633nm)" package="5 mm [THT]"]
  R1 = Resistor [tolerance=±5% resistance=220 package=THT]
  R2 = Resistor [tolerance=±5% resistance=100 package=THT]
  R3 = Resistor [tolerance=±5% resistance=10k package=THT]

nets:
  N1: Componente1.A0, R3.Pin_0
  N2: Componente1.5V, R2.Pin_0, R3.Pin_1
  N3: Componente1.GND, LED1.anode
  N4: Componente1.D2_PWM, R1.Pin_0
  N5: LED1.cathode, R1.Pin_1
