# Fritzing sketch id1595_HandheldShield_0 (saved by Fritzing 0.9.3b)
circuit board: 11.4cm x 5.64cm
breadboards: 1

parts:
  MAX485 = MAX485 [package=dil08]
  Part1 = Arduino Mega ADK (Rev3)
  UP = Pushbutton [package="[THT]"]
  DOWN = Pushbutton [package="[THT]"]
  LEFT = Pushbutton [package="[THT]"]
  RIGHT = Pushbutton [package="[THT]"]
  KEY1 = Pushbutton [package="[THT]"]
  KEY2 = Pushbutton [package="[THT]"]
  KEY3 = Pushbutton [package="[THT]"]
  KEYC = Pushbutton [package="[THT]"]
  KEY5 = Pushbutton [package="[THT]"]
  KEY6 = Pushbutton [package="[THT]"]
  KEY4 = Pushbutton [package="[THT]"]
  KEY8 = Pushbutton [package="[THT]"]
  KEY9 = Pushbutton [package="[THT]"]
  KEYE = Pushbutton [package="[THT]"]
  KEY7 = Pushbutton [package="[THT]"]
  KEY0 = Pushbutton [package="[THT]"]
  KEY# = Pushbutton [package="[THT]"]
  KEYF = Pushbutton [package="[THT]"]
  KEY* = Pushbutton [package="[THT]"]
  KEYA = Pushbutton [package="[THT]"]
  KEYB = Pushbutton [package="[THT]"]
  DISPLAY = rounded female pin header, 8 pins [form="♀ (female rounded)"]
  KEYD = Pushbutton [package="[THT]"]
  RJ45 = RJ45 Jack [package=rj45-8]
  RS232 = screw terminal, 3 pins
  RS485 = screw terminal, 3 pins
  XNET = RJ11 Jack [package=rj11-6]
  POWER = screw terminal, 3 pins
  J1 = female pin header, 2 pins [form="♀ (female)"]

nets:
  RX2: MAX485.RO, Part1.D17/RX2
  RTS: MAX485.RE, MAX485.DE, Part1.D2_PWM
  TX2: MAX485.DI, Part1.D16/TX2
  GND: MAX485.GND, Part1.GND, DISPLAY.pin8, RJ45.7, RS232.pin3, RS485.pin3, XNET.1, POWER.pin3
  N1: MAX485.A, RS485.pin1, XNET.2
  N2: MAX485.B, RS485.pin2, XNET.6
  5V: MAX485.VCC, Part1.IOREF, Part1.5V, DISPLAY.pin7, RJ45.4, POWER.pin2
  SCL: Part1.D21/SCL, RJ45.1
  SDA: Part1.D20/SDA, RJ45.3
  RX1: Part1.D19/RX1, RS232.pin2
  TX1: Part1.D18/TX1, RS232.pin1
  RX3: Part1.D15/RX3, RJ45.2
  TX3: Part1.D14/TX3, RJ45.6
  12V: Part1.VIN, POWER.pin1, J1.pin1
  ROW0: Part1.D22, UP.Pin_4, LEFT.Pin_3, LEFT.Pin_4, KEYA.Pin_3, KEYA.Pin_4
  ROW1: Part1.D24, DOWN.Pin_3, DOWN.Pin_4, RIGHT.Pin_3, RIGHT.Pin_4, KEYB.Pin_3, KEYB.Pin_4
  ROW2: Part1.D26, KEY1.Pin_3, KEY1.Pin_4, KEY2.Pin_3, KEY2.Pin_4, KEY3.Pin_3, KEY3.Pin_4, KEYC.Pin_3, KEYC.Pin_4
  ROW3: Part1.D28, KEY5.Pin_3, KEY5.Pin_4, KEY6.Pin_3, KEY6.Pin_4, KEY4.Pin_3, KEY4.Pin_4, KEYD.Pin_3, KEYD.Pin_4
  ROW4: Part1.D30, KEY8.Pin_3, KEY8.Pin_4, KEY9.Pin_3, KEY9.Pin_4, KEYE.Pin_3, KEYE.Pin_4, KEY7.Pin_3, KEY7.Pin_4
  ROW5: Part1.D32, KEY0.Pin_3, KEY0.Pin_4, KEY#.Pin_3, KEY#.Pin_4, KEYF.Pin_3, KEYF.Pin_4, KEY*.Pin_3, KEY*.Pin_4
  COL5: Part1.D34, KEYC.Pin_1, KEYE.Pin_1, KEYE.Pin_2, KEYF.Pin_1, KEYF.Pin_2, KEYD.Pin_1, KEYD.Pin_2
  COL4: Part1.D36, KEY3.Pin_1, KEY3.Pin_2, KEY6.Pin_1, KEY6.Pin_2, KEY9.Pin_1, KEY9.Pin_2, KEY#.Pin_1, KEY#.Pin_2
  COL3: Part1.D38, KEY2.Pin_1, KEY5.Pin_1, KEY5.Pin_2, KEY8.Pin_1, KEY8.Pin_2, KEY0.Pin_1, KEY0.Pin_2
  COL0: Part1.D40, DOWN.Pin_2, KEYA.Pin_1, KEYA.Pin_2
  COL1: Part1.D42, LEFT.Pin_1, LEFT.Pin_2, RIGHT.Pin_1, RIGHT.Pin_2
  COL2: Part1.D44, UP.Pin_1, UP.Pin_2, KEY1.Pin_1, KEY4.Pin_1, KEY4.Pin_2, KEY7.Pin_1, KEY7.Pin_2, KEY*.Pin_1, KEY*.Pin_2, KEYB.Pin_1, KEYB.Pin_2
  RES: Part1.D46, DISPLAY.pin4
  CS: Part1.D47, DISPLAY.pin2
  DC: Part1.D48, DISPLAY.pin3
  MOSI: Part1.D51/MOSI, DISPLAY.pin5
  SCK: Part1.D52/SCK, DISPLAY.pin6
  BL: DISPLAY.pin1
  N3: XNET.3, J1.pin2

notes:
  A2
  B2
  GND
  RX1
  TX1
  5V
  Vin
  SCK
  MOSI
  RES
  DC
  CS
