# Fritzing sketch id1596_EQDirect_BTx3_0 (saved by Fritzing 0.9.2b)
circuit board: 3.46351cm x 4.14105cm
breadboards: 1

parts:
  R1 = Resistor [tolerance=±5% resistance=4.7k package=THT]
  R2 = Resistor [tolerance=±5% resistance=10k package=THT]
  R3 = Resistor [tolerance=±5% resistance=10k package=THT]
  R4 = Resistor [tolerance=±5% resistance=10k package=THT]
  R5 = Resistor [tolerance=±5% resistance=10k package=THT]
  R6 = Resistor [tolerance=±5% resistance=10k package=THT]
  IC1 = my7805 [part_number=7805]
  Q1 = my2n7000 [part_number=2N7000]
  Q2 = my2n7000 [part_number=2N7000]
  X1 = DB9 Connector [part_number="EQ6 MOUNT" package=db9]
  JP1 = Header 6 [part_number=HC-05 package=molex-1x6-ra]
  LED1 = LED - 3mm [color="Red (633nm)" package="3 mm [THT]"]
  R7 = Resistor [tolerance=±5% resistance=220 package=THT]

nets:
  N1: R1.Pin_0, R2.Pin_1, R3.Pin_1, R5.Pin_1, Q1.connector1, Q2.connector1
  N2: R1.Pin_1, R4.Pin_1, R6.Pin_1, IC1.connector2, JP1.5, R7.Pin_1
  GND: R2.Pin_0, IC1.connector0, X1.5, JP1.4, LED1.cathode
  N3: R3.Pin_0, Q1.connector0, JP1.2
  N4: R4.Pin_0, Q1.connector2, X1.9
  N5: R5.Pin_0, Q2.connector0, JP1.3
  N6: R6.Pin_0, Q2.connector2, X1.6
  N7: IC1.connector1, X1.1
  N8: LED1.anode, R7.Pin_0

notes:
  RX
  TX
  GND
  +5V
  EQDIRECT-BT-V1
  indstronomy.com
  5V
  INDSTRONOMY
  EQDIRECT BLUETOOTH ADAPTER
  http://indstronomy.com
