# Fritzing sketch id1597_Joystick_Control_0 (saved by Fritzing 0.9.3b)
circuit board: 8.46667cm x 5.64444cm

parts:
  Part1 = Arduino Uno (Rev3)
  Part2 = Thumb Joystick

nets:
  N1: Part1.A0, Part2.HORZ
  N2: Part1.A1, Part2.VERT
  GND: Part1.GND, Part2.GND
  N3: Part1.D2, Part2.SEL
  5V: Part1.5V, Part2.VCC
