# Fritzing sketch id1598_Escape_Room_Box_0 (saved by Fritzing 0.9.3b)
breadboards: 2
stripboards: 2

parts:
  Part1 = Arduino Nano (Rev3.0) (ICSP)
  Power_plug1 = Power plug
  Q1 = NPN-Transistor [package="TO92 [THT]"]
  L1 = Solenoid  # not connected
  D1 = Rectifier Diode [part_number=1N4001 package="300 mil [THT]"]
  U1 = mystery part, 2 pins [chip_label="LASER DIODE"]
  U2 = mystery part, 2 pins [chip_label="LASER DIODE"]
  U3 = mystery part, 2 pins [chip_label="LASER DIODE"]
  U4 = mystery part, 2 pins [chip_label="LASER DIODE"]
  Q2 = NPN-Transistor [package="TO92 [THT]"]
  Power_plug2 = Power plug
  LED1 = LED - 5mm [color="Red (633nm)" package="5 mm [THT]"]
  LED2 = LED - 5mm [color="Red (633nm)" package="5 mm [THT]"]
  Power_plug3 = Power plug
  R4 = Resistor [tolerance=±5% resistance=220 package=THT]
  S1 = Reed switch [package=THT]
  S2 = Reed switch [package=THT]
  S3 = Reed switch [package=THT]
  S4 = Reed switch [package=THT]

nets:
  GND: Part1.GND, Power_plug1.GND, D1.anode, Power_plug2.GND, R4.Pin_0, S1.pin_2
  N1: Part1.D3, S4.pin_2
  N2: Part1.D7, LED1.anode
  N3: Part1.D9, LED2.anode
  N4: Part1.D12/MISO, Q1.B
  VIN: Part1.VIN, Power_plug1.VCC
  N5: Part1.5V, Q1.C, Q2.C
  N6: Part1.D13/SCK, Q2.B
  N7: Q1.E, D1.cathode
  N8: U1.pin1, U2.pin1, U3.pin1, U4.pin1, Power_plug3.VCC
  N9: U1.pin2, U2.pin2, U3.pin2, U4.pin2, Power_plug3.GND
  N10: Q2.E, Power_plug2.VCC
  N11: LED1.cathode, LED2.cathode, R4.Pin_1
  N12: S1.pin_1, S2.pin_1
  N13: S2.pin_2, S3.pin_1
  N14: S3.pin_2, S4.pin_1
