# Fritzing sketch id159_555_timer_0 (saved by Fritzing 0.9.3b)
breadboards: 3

parts:
  R1 = Resistor [tolerance=±5% resistance=10k package=THT]
  BAT1 = BC9VPC [package=bc9vpc]
  C1 = Electrolytic Capacitor [capacitance=470µF package="0605 [SMD, electrolytic]"]
  LED1 = smd LED [color="Red (633nm)" package="0603 [SMD]"]
  S1 = Pushbutton [package="[SMD]"]
  R2 = Resistor [tolerance=±5% resistance=10k package=THT]
  R3 = Resistor [tolerance=±5% resistance=470 package=THT]
  BAT2 = BC9VPC [package=bc9vpc]
  U2 = 555 Timer [package="DIP8 [THT]"]
  U3 = 555 Timer [package="DIP8 [THT]"]
  C3 = Electrolytic Capacitor [capacitance=0.01µF package="0605 [SMD, electrolytic]"]
  C5 = Electrolytic Capacitor [capacitance=0.01µF package="0605 [SMD, electrolytic]"]
  LED2 = smd LED [color="Red (633nm)" package="0603 [SMD]"]
  R4 = Resistor [tolerance=±5% resistance=470 package="2010 [SMD]"]
  R5 = Resistor [tolerance=±5% resistance=10k package=THT]
  R6 = Resistor [tolerance=±5% resistance=10k package=THT]
  BAT3 = BC9VPC [package=bc9vpc]
  U4 = 555 Timer [package="DIP8 [THT]"]
  C6 = Electrolytic Capacitor [capacitance=0.01µF package="0605 [SMD, electrolytic]"]
  LED3 = smd LED [color="Red (633nm)" package="0603 [SMD]"]
  R8 = Resistor [tolerance=±5% resistance=1k package=THT]
  R9 = Resistor [tolerance=±5% resistance=4.7k package=THT]
  R10 = Resistor [tolerance=±5% resistance=4.7k package=THT]
  S3 = Momentary Switch [package=ksa_sealed_tac_switch]
  S4 = Pushbutton [package="[THT]"]

nets:
  N1: R1.Pin_0, BAT1.V+, R2.Pin_1, U2.Vcc_Supply_Voltage
  N2: R1.Pin_1, C1.-, U2.Threshold, U2.Discharge
  N3: BAT1.V-, C1.+, S1.Pin_1, S1.Pin_2, R3.Pin_0, U2.Ground, C5.+
  N4: LED1.cathode, U2.Output
  N5: LED1.anode, R3.Pin_1
  N6: S1.Pin_3, S1.Pin_4, R2.Pin_0, U2.Trigger
  N7: BAT2.V+, U3.Vcc_Supply_Voltage, R5.Pin_1, R6.Pin_1
  N8: BAT2.V-, U3.Ground, U3.Threshold, C3.-, R4.Pin_1, S3.2, S4.Pin_1, S4.Pin_2
  N9: U2.Control_Voltage, C5.-
  N10: U3.Trigger, R6.Pin_0, S4.Pin_3, S4.Pin_4
  N11: U3.Output, LED2.cathode
  N12: U3.Reset, S3.4
  N13: U3.Control_Voltage, C3.+
  N14: LED2.anode, R4.Pin_0
  N15: R5.Pin_0, S3.3
  N16: BAT3.V+, U4.Reset, U4.Vcc_Supply_Voltage, R10.Pin_1
  N17: BAT3.V-, U4.Ground, C6.-, LED3.cathode
  N18: U4.Trigger, U4.Threshold, C6.+, R9.Pin_1
  N19: U4.Output, R8.Pin_1
  N20: U4.Discharge, R9.Pin_0, R10.Pin_0
  N21: LED3.anode, R8.Pin_0
