# Fritzing sketch id1600_ESP07_Daughterboard_V0_1_0 (saved by Fritzing 0.9.3b)
circuit board: 3.2cm x 2.6cm
breadboards: 1

parts:
  ESP-12E = ESP8266 WiFi Module [part_number=ESP8266]
  C2 = Capacitor [package=1206]
  1k = Resistor [tolerance=±5% resistance=220 package="1206 [SMD]"]
  R2 = Resistor [tolerance=±5% resistance=10k package="1206 [SMD]"]
  R3 = Resistor [tolerance=±5% resistance=220 package="1206 [SMD]"]
  C3 = Capacitor [package=1206]
  R4 = Resistor [tolerance=±5% resistance=220 package="1206 [SMD]"]
  Pad1 = Pad [width=1 height=1.8 connect=center]
  Pad2 = Pad [width=1 height=1.8 connect=center]
  Pad3 = Pad [width=1 height=1.8 connect=center]
  Pad4 = Pad [width=1 height=1.8 connect=center]
  Pad5 = Pad [width=1 height=1.8 connect=center]
  Pad6 = Pad [width=1 height=1.8 connect=center]
  R--GND-G--B1 = double row female pin header, 22 pins [form="♀ (female)"]
  TX-RX-GND-5v = female pin header, 4 pins [form="♀ (female)"]
  U1 = Voltage Regulator LM1117 [package=sot223]

nets:
  N1: ESP-12E.RXD, TX-RX-GND-5v.pin3
  N2: ESP-12E.VCC, 1k.Pin_0, C3.2, R4.Pin_1, R--GND-G--B1.pin18, U1.OUT
  N3: ESP-12E.GPIO_0, R--GND-G--B1.pin1
  N4: ESP-12E.GPIO_2, R--GND-G--B1.pin2
  N5: ESP-12E.CH_PD, R4.Pin_0, R--GND-G--B1.pin15
  N6: ESP-12E.GND, C2.1, R2.Pin_0, R3.Pin_1, C3.1, R--GND-G--B1.pin3, TX-RX-GND-5v.pin2, U1.ADJ
  N7: ESP-12E.TXD, TX-RX-GND-5v.pin4
  N8: ESP-12E.GPIO_15, R3.Pin_0
  N9: ESP-12E.GPIO_4, R--GND-G--B1.pin21
  N10: ESP-12E.GPIO_5, R--GND-G--B1.pin22
  N11: ESP-12E.ADC_0, R2.Pin_1, R--GND-G--B1.pin16
  N12: ESP-12E.GPIO_16, R--GND-G--B1.pin14
  N13: ESP-12E.GPIO_14, R--GND-G--B1.pin10
  N14: ESP-12E.GPIO_12, R--GND-G--B1.pin12
  N15: ESP-12E.GPIO_13, R--GND-G--B1.pin11
  N16: ESP-12E.REST, C2.2, 1k.Pin_1, R--GND-G--B1.pin17
  N17: Pad1.pad, R--GND-G--B1.pin9
  N18: Pad2.pad, R--GND-G--B1.pin8
  N19: Pad3.pad, R--GND-G--B1.pin7
  N20: Pad4.pad, R--GND-G--B1.pin6
  N21: Pad5.pad, R--GND-G--B1.pin5
  N22: Pad6.pad, R--GND-G--B1.pin4
  N23: R--GND-G--B1.pin20, TX-RX-GND-5v.pin1, U1.IN

notes:
  ESP-12E Daughter Board
  Version 0.1
  Designed by Ross Kopp
  PIN 1
  PIN 11
  PIN 22
  PIN 12
  Programming Header
