# Fritzing sketch id1601_Main_Board_V0_1_0 (saved by Fritzing 0.9.3b)
circuit board: 7.3cm x 4.3cm
breadboards: 1

parts:
  R--GND-G--B3 = double row female pin header, 22 pins [form="♀ (female)"]
  NEU---HOT = screw terminal, 2 pins
  R--GND-G--B4 = double row female pin header, 10 pins [form="♀ (female)"]
  500mA_Fuse = Resettable Fuse PTC [package=ptc]
  R--GND-G--B5 = double row female pin header, 10 pins [form="♀ (female)"]
  3v3_1117 = Voltage Regulator LM1117 [package=sot223]
  R--GND-G--B7 = female pin header, 5 pins [form="♀ (female)"]
  PRGM_SWITCH = SPST Switch [package=switch-spdt_kit]
  Reset_Button_ESP = Pushbutton [package="[THT]"]
  R--GND-G--B8 = double row female pin header, 6 pins [form="♀ (female)"]
  R--GND-G--B9 = female pin header, 5 pins [form="♀ (female)"]

nets:
  N1: R--GND-G--B3.pin1, R--GND-G--B4.pin3
  N2: R--GND-G--B3.pin2, R--GND-G--B4.pin2
  N3: R--GND-G--B3.pin3, R--GND-G--B4.pin5, R--GND-G--B5.pin10, 3v3_1117.IN, R--GND-G--B7.pin1, R--GND-G--B8.pin1, R--GND-G--B8.pin2, R--GND-G--B8.pin3, R--GND-G--B9.pin1
  N4: R--GND-G--B3.pin5, PRGM_SWITCH.O
  N5: R--GND-G--B3.pin6, Reset_Button_ESP.Pin_1, Reset_Button_ESP.Pin_2
  N6: R--GND-G--B3.pin7, R--GND-G--B7.pin4
  N7: R--GND-G--B3.pin9, R--GND-G--B9.pin4
  N8: R--GND-G--B3.pin11, R--GND-G--B9.pin5
  N9: R--GND-G--B3.pin12, R--GND-G--B5.pin9
  N10: R--GND-G--B3.pin13, R--GND-G--B5.pin8
  N11: R--GND-G--B3.pin14, R--GND-G--B4.pin10, R--GND-G--B5.pin5
  N12: R--GND-G--B3.pin15, R--GND-G--B4.pin9, R--GND-G--B5.pin4
  N13: R--GND-G--B3.pin16, R--GND-G--B5.pin7
  N14: R--GND-G--B3.pin17, R--GND-G--B4.pin1, R--GND-G--B5.pin6, R--GND-G--B7.pin5
  N15: R--GND-G--B3.pin18, R--GND-G--B4.pin8, R--GND-G--B5.pin3
  N16: R--GND-G--B3.pin19, R--GND-G--B4.pin7, R--GND-G--B5.pin2
  N17: R--GND-G--B3.pin20, R--GND-G--B4.pin6, R--GND-G--B5.pin1, 3v3_1117.ADJ, R--GND-G--B7.pin3, PRGM_SWITCH.S, Reset_Button_ESP.Pin_3, Reset_Button_ESP.Pin_4, R--GND-G--B8.pin4, R--GND-G--B8.pin5, R--GND-G--B8.pin6, R--GND-G--B9.pin3
  N18: R--GND-G--B3.pin21, R--GND-G--B4.pin4
  N19: R--GND-G--B3.pin22, PRGM_SWITCH.P
  N20: NEU---HOT.pin2, 500mA_Fuse.1
  N21: 3v3_1117.OUT, R--GND-G--B7.pin2, R--GND-G--B9.pin2

notes:
  MISO
  MOSI
  GPIO 04
  Unused
  GPIO 09
  DS TEMP 10
  SCLK
  5 VDC +
  GPIO 12
  GPIO 14
  GPIO 05
  Reset
  CS0
  GPIO 00
  3.3 VDC +
  GPIO 13
  ADC/Analog
  GPIO 02
  5 VDC -
  CH/PD
  GPIO 16
  5 VDC-
  CS 0
  DS TEMP
  ADC
  GND -
  ESP Mainboard
  SLOT 2
  SLOT 1
  Temp/Light
  Module
  Designed by Ross Kopp
  Version 0.1
  ESP-12E MainBoard
