# Fritzing sketch id1602_RGB_LED_Daughterboard_V0_1_0 (saved by Fritzing 0.9.3b)
circuit board: 3.2cm x 2.6cm
breadboards: 1

parts:
  LED1 = RGB LED (com. cathode, rgb) [package="5 mm [THT]"]
  LED2 = RGB LED (com. cathode, rgb) [package="5 mm [THT]"]
  ATTiny85 = attiny85 [package=dip]
  PNP_Blu = PNP-Transistor [package="SOT-23 [SMD]"]
  PNP_Gre = PNP-Transistor [package="SOT-23 [SMD]"]
  PNP_Red = PNP-Transistor [package="SOT-23 [SMD]"]
  1k = Resistor [tolerance=±5% resistance=220 package="1206 [SMD]"]
  1k_2 = Resistor [tolerance=±5% resistance=220 package="1206 [SMD]"]
  1k_3 = Resistor [tolerance=±5% resistance=220 package="1206 [SMD]"]
  NPN_Ground = NPN-Transistor [package="SOT-23 [SMD]"]
  R--GND-G--B2 = double row female pin header, 10 pins [form="♀ (female)"]
  3v3_Regulator = Voltage Regulator LM1117 [package=sot223]
  PNP_Power = PNP-Transistor [package="TO92 [THT]"]
  1k_4 = Resistor [tolerance=±5% resistance=220 package="1206 [SMD]"]
  Temp_Sensor = DS18B20 1-Wire Temperature Sensor [part_number=DS18B20]
  4k7 = Resistor [tolerance=±5% resistance=220 package="1206 [SMD]"]

nets:
  N1: LED1.red_anode, LED2.red_anode, PNP_Red.2
  N2: LED1.common_cathode, LED2.common_cathode, NPN_Ground.2, R--GND-G--B2.pin10, 3v3_Regulator.ADJ, Temp_Sensor.GND
  N3: LED1.green_anode, LED2.green_anode, PNP_Blu.2
  N4: LED1.blue_anode, LED2.blue_anode, PNP_Gre.2
  N5: ATTiny85.Pin_2, ATTiny85.Pin_4, NPN_Ground.1
  N6: ATTiny85.Pin_5, 1k_2.Pin_1
  N7: ATTiny85.Pin_6, 1k.Pin_1
  N8: ATTiny85.Pin_7, 1k_3.Pin_1
  N9: ATTiny85.Pin_8, NPN_Ground.0, 3v3_Regulator.IN, PNP_Power.E
  N10: PNP_Blu.0, 1k_2.Pin_0
  N11: PNP_Blu.1, PNP_Gre.1, PNP_Red.1, 3v3_Regulator.OUT
  N12: PNP_Gre.0, 1k.Pin_0
  N13: PNP_Red.0, 1k_3.Pin_0
  N14: R--GND-G--B2.pin1, PNP_Power.C, Temp_Sensor.VDD, 4k7.Pin_0
  N15: R--GND-G--B2.pin2, 1k_4.Pin_0
  N16: R--GND-G--B2.pin5, Temp_Sensor.DQ, 4k7.Pin_1
  N17: PNP_Power.B, 1k_4.Pin_1

notes:
  Designed by Ross Kopp
  Version 0.1
  LEC Controller Daughter Board
