# Fritzing sketch id1603_TEMP_LIGHT_Daughterboard_V0_1_0 (saved by Fritzing 0.9.3b)
circuit board: 2cm x 2cm
breadboards: 1

parts:
  Photocell_3v3 = PHOTOCELL [package=photocell]
  R--GND-G--B6 = female pin header, 5 pins [form="♀ (female)"]
  DS18b20_or_DHT22 = female pin header, 3 pins [form="♀ (female)"]
  4k7 = Resistor [tolerance=±5% resistance=4.7k package="1206 [SMD]"]
  DS1 = DS18B20 1-Wire Temperature Sensor [part_number=DS18B20]
  PhotoResistor = female pin header, 2 pins [form="♀ (female)"]

nets:
  N1: Photocell_3v3.P$1, R--GND-G--B6.pin4, PhotoResistor.pin1
  N2: Photocell_3v3.P$2, R--GND-G--B6.pin2, PhotoResistor.pin2
  N3: R--GND-G--B6.pin1, DS18b20_or_DHT22.pin1, 4k7.Pin_1, DS1.VDD
  N4: R--GND-G--B6.pin3, DS18b20_or_DHT22.pin3, DS1.GND
  N5: R--GND-G--B6.pin5, DS18b20_or_DHT22.pin2, 4k7.Pin_0, DS1.DQ

notes:
  ADC
  GND -
  3.3 VDC +
  5 VDC +
  DS TEMP 10
  DS TEMP
  Designed by Ross Kopp
  Version 0.1
  Light and Temp DaughterBoard
