# Fritzing sketch id1604_ch340g_esp12e_2_0 (saved by Fritzing 0.9.3b)
circuit board: 7cm x 6cm
breadboards: 1

parts:
  USB3 = USB Connectors [package=usb-b-pth]
  12000 = Crystal [frequency="16 Mhz" package=THT]
  100nF = Capacitor [package=axial-5mm]
  100nF_2 = Capacitor [package=axial-5mm]
  22pF = Capacitor [package=axial-5mm]
  22pF_2 = Capacitor [package=axial-5mm]
  CH340G = SO16 [chip_label=CH340G package=SO]
  LM1117 = Voltage Regulator LM1117 [package=sot223]
  10uF = Capacitor Polarized [package=cpol-radial-10uf-25v]
  10uF_2 = Capacitor Polarized [package=cpol-radial-10uf-25v]
  PWR = smd LED [color="Red (633nm)" package="0805 [SMD]"]
  2K = Resistor [tolerance=±5% resistance=220 package="0805 [SMD]"]
  103 = Resistor [tolerance=±5% resistance=10k package="0805 [SMD]"]
  103_2 = Resistor [tolerance=±5% resistance=10k package="0805 [SMD]"]
  103_3 = Resistor [tolerance=±5% resistance=10k package="0805 [SMD]"]
  103_4 = Resistor [tolerance=±5% resistance=10k package="0805 [SMD]"]
  Reset = Pushbutton [package="[THT]"]
  Flash = Pushbutton [package="[THT]"]

nets:
  N1: USB3.D+, CH340G.5
  N2: USB3.D-, CH340G.6
  N3: USB3.GND, 100nF.2, 100nF_2.2, 22pF.2, 22pF_2.2, CH340G.1, LM1117.ADJ, 10uF.-, 10uF_2.-, 103_4.Pin_0, Reset.Pin_3, Reset.Pin_4, Flash.Pin_1, Flash.Pin_2
  N4: USB3.VBUS, 100nF_2.1, CH340G.16, LM1117.IN, 10uF.+, PWR.anode
  N5: 12000.pin_0, 22pF_2.1, CH340G.8
  N6: 12000.pin_1, 22pF.1, CH340G.7
  N7: 100nF.1, CH340G.4
  N8: CH340G.13, 103_2.Pin_1, Flash.Pin_3, Flash.Pin_4
  N9: CH340G.14, 103.Pin_1, Reset.Pin_1, Reset.Pin_2
  N10: LM1117.OUT, 10uF_2.+, 103.Pin_0, 103_2.Pin_0, 103_3.Pin_1
  N11: PWR.cathode, 2K.Pin_0

notes:
  GND
  VCC
  NC
  5V
  TX
  RX
  DTR
  SCL
  SDA
  V+
  V-
  D-
  D+
  A0
  3V
  RTS
  MOSI(DIN)
  D15
  SCK(CLK)
  D4
  D5
  3V3
  IO2
  IO0
  RST
  CHPD
  MISO(DOUT)
  D16
  ADC
  D1
  D3
  D0
  D2
  SDA/D4
  SCL/D5
  DIN/D13
  CS/D15
  CLK/D14
  SPI
  I2C
  ----5V----
  ----3V----
  SDA/D0
  SCL/D2
  ----GND----
  ---------------------------------------
  -------------------
  -------------------------------
  TX0  D1
  D1/TX
  D3/RX
  D12
  ESP-12E
  ESP-01
  CS
  RX0
  TX0
  D14
  D13
  DOUT
  ESP-Programmer
  (C) Rene Wennekes
