# Fritzing sketch id1605_Untitled_Sketch_2_0 (saved by Fritzing 0.9.3b)
breadboards: 1

parts:
  U1 = ESP8266 WiFi Module [part_number=ESP8266]
  Q1 = PNP-Transistor [package="SOT-23 [SMD]"]
  Q2 = PNP-Transistor [package="SOT-23 [SMD]"]
  Q3 = PNP-Transistor [package="SOT-23 [SMD]"]
  R1 = Resistor [tolerance=±5% resistance=220 package=THT]
  R2 = Resistor [tolerance=±5% resistance=220 package=THT]
  R3 = Resistor [tolerance=±5% resistance=220 package=THT]
  LED1 = RGB LED (com. cathode, rgb) [package="5 mm [THT]"]

nets:
  N1: U1.IO2, R3.Pin_0
  N2: U1.D0, R2.Pin_0
  N3: U1.3.3V#10, R1.Pin_0
  N4: Q1.2, Q2.2, Q3.2
  N5: Q1.1, LED1.green_anode
  N6: Q2.1, LED1.common_cathode
  N7: Q3.1, LED1.red_anode
