# Fritzing sketch id1606_esp01_devboard_0 (saved by Fritzing 0.9.3b)
circuit board: 6.93653cm x 5.21609cm
perfboards: 1

parts:
  GND = female pin header, 4 pins [form="♀ (female)"]
  3_3V = female pin header, 4 pins [form="♀ (female)"]
  PIN = female pin header, 4 pins [form="♀ (female)"]
  J4 = female pin header, 4 pins [form="♀ (female)"]
  J5 = female pin header, 4 pins [form="♀ (female)"]
  GND_R_T = female pin header, 5 pins [form="♀ (female)"]
  load = Dagu DGServo 9g header (male) [package=THT]
  LM317T = Voltage Regulator - Variable [package="TO220 [THT]"]
  R1 = Resistor [tolerance=±5% resistance=5.6k package=THT]
  R2 = Resistor [tolerance=±5% resistance=10k package=THT]
  R3 = Resistor [tolerance=±5% resistance=10k package=THT]
  R4 = Resistor [tolerance=±5% resistance=3.3k package=THT]
  RESET = Pushbutton [package=THT]
  VCC_+_gnd = Battery block 9V
  C1 = Electrolytic Capacitor [capacitance=10µF package="100 mil [THT, electrolytic]"]
  R5 = Resistor [tolerance=±5% resistance=10k package=THT]

nets:
  N1: GND.pin1, GND.pin2, GND.pin3, GND.pin4, J4.pin4, LM317T.OUT, R2.Pin_0, R3.Pin_0, R4.Pin_1, C1.+, R5.Pin_1
  N2: 3_3V.pin1, 3_3V.pin2, 3_3V.pin3, 3_3V.pin4, J5.pin1, GND_R_T.pin1, load.gnd, R1.Pin_1, RESET.leg1, VCC_+_gnd.-, C1.-
  N3: PIN.pin1, J5.pin3, load.Vcc
  N4: PIN.pin2, J4.pin1, GND_R_T.pin2
  N5: PIN.pin3, J5.pin4, GND_R_T.pin3
  N6: PIN.pin4, J5.pin2
  N7: J4.pin2, R3.Pin_1
  N8: J4.pin3, R2.Pin_1, RESET.leg0
  N9: load.pulse, R5.Pin_0
  N10: LM317T.ADJ, R1.Pin_0, R4.Pin_0
  N11: LM317T.IN, VCC_+_gnd.+

notes:
  adapter
  mode switch
  expansion
  reset
  0 1 3 2
  +
