# Fritzing sketch id1607_Switch_0 (saved by Fritzing 0.9.3b)
circuit board: 4.5cm x 4.5cm
breadboards: 1

parts:
  1117 = AMS1117
  C1 = Electrolytic Capacitor [capacitance=1µF package="100 mil [THT, electrolytic]"]
  C2 = Electrolytic Capacitor [capacitance=1µF package="100 mil [THT, electrolytic]"]
  U1 = ESP-12F [part_number=ESP8266]
  R1 = Resistor [tolerance=±5% resistance=10k package=THT]
  R2 = Resistor [tolerance=±5% resistance=220 package=THT]
  R3 = Resistor [tolerance=±5% resistance=220 package=THT]
  U2 = Sharp PC817 [package=THT]
  Q1 = NPN-Transistor [package="TO92 [THT]"]
  R4 = Resistor [tolerance=±5% resistance=220 package=THT]
  R5 = Resistor [tolerance=±5% resistance=220 package=THT]

nets:
  N1: 1117.connector0, C1.-, C2.-, U1.connector6, R3.Pin_1, U2.Pin_2, Q1.E, R5.Pin_0
  N2: 1117.connector1, C1.+, U1.connector1, R1.Pin_1
  N3: 1117.connector2, C2.+, U2.Pin_4, R5.Pin_1
  N4: U1.connector5, R1.Pin_0
  N5: U1.connector10, R2.Pin_0
  N6: R2.Pin_1, U2.Pin_1
  N7: R3.Pin_0, U2.Pin_3, R4.Pin_0
  N8: Q1.B, R4.Pin_1

notes:
  G
  5
  3
  R
