# Fritzing sketch id1608_esp12_artik_0 (saved by Fritzing 0.9.3b)
breadboards: 1

parts:
  Gizwits_WiFi_Witty_ESP-12F1 = Gizwits WiFi Witty ESP-12F
  Part1 = FTDI Basic Programmer
  R1 = Resistor [tolerance=±5% resistance=10k package="0603 [SMD]"]
  S3 = Pushbutton [package="[SMD]"]
  S4 = Pushbutton [package="[SMD]"]

nets:
  GND: Gizwits_WiFi_Witty_ESP-12F1.REST, Gizwits_WiFi_Witty_ESP-12F1.GND, Part1.GND, R1.Pin_1, S3.Pin_1, S3.Pin_2, S4.Pin_1, S4.Pin_2
  N1: Gizwits_WiFi_Witty_ESP-12F1.GPIO4, R1.Pin_0
  N2: Gizwits_WiFi_Witty_ESP-12F1.RXD, Part1.TXO
  N3: Gizwits_WiFi_Witty_ESP-12F1.TXD, Part1.RXI
  N4: S3.Pin_3, S3.Pin_4
  N5: S4.Pin_3, S4.Pin_4
