# Fritzing sketch id160_555+4017_0 (saved by Fritzing 0.8.5b)
breadboards: 1

parts:
  U1 = 555 Timer [package="DIP8 [THT]"]
  C1 = Electrolytic Capacitor [capacitance=1µF package="100 mil [THT, electrolytic]"]
  R1 = Resistor [tolerance=±5% resistance=10k package=THT]
  LED1 = LED - 5mm [color="Red (633nm)" package="5 mm [THT]"]
  R3 = Resistor [tolerance=±5% resistance=220 package=THT]
  IC1 = IC, DIP package, 16 pins [chip_label=4017]
  LED2 = LED - 5mm [color="Red (633nm)" package="5 mm [THT]"]
  R4 = Resistor [tolerance=±5% resistance=220 package=THT]
  LED3 = LED - 5mm [color="Green (565nm)" package="5 mm [THT]"]
  R5 = Resistor [tolerance=±5% resistance=220 package=THT]
  LED4 = LED - 5mm [color="Red (633nm)" package="5 mm [THT]"]
  LED5 = LED - 5mm [color="Green (560nm)" package="5 mm [THT]"]
  R6 = Resistor [tolerance=±5% resistance=220 package=THT]
  R7 = Resistor [tolerance=±5% resistance=220 package=THT]
  R2 = Rotary Potentiometer (Large) [maximum_resistance=100kΩ package=THT]

nets:
  GND: U1.Ground, C1.-, R3.Pin_1, IC1.pin8, IC1.pin13, R4.Pin_0, R5.Pin_0, R6.Pin_0, R7.Pin_0
  N1: U1.Trigger, U1.Threshold, C1.+, R2.wiper
  N2: U1.Output, LED1.anode, IC1.pin14
  12V: U1.Reset, U1.Vcc_Supply_Voltage, R1.Pin_0, IC1.pin16
  N3: U1.Discharge, R1.Pin_1, R2.leg1
  N4: LED1.cathode, R3.Pin_0
  N5: IC1.pin2, LED3.anode
  N6: IC1.pin3, LED2.anode
  N7: IC1.pin4, LED4.anode
  N8: IC1.pin7, LED5.anode
  N9: IC1.pin10, IC1.pin15
  N10: LED2.cathode, R4.Pin_1
  N11: LED3.cathode, R5.Pin_1
  N12: LED4.cathode, R7.Pin_1
  N13: LED5.cathode, R6.Pin_1
