# Fritzing sketch id1611_esp8266_use_0 (saved by Fritzing 0.9.1b)
circuit board: 4.19193cm x 3.35844cm
breadboards: 1

parts:
  Power_plug1 = Power plug
  Adj_Vout_Vin = Voltage Regulator [package=to220-adj]
  J1 = female pin header, 4 pins [form="♀ (female)"]  # not connected
  VCC--RST--CH_P--TX = female pin header, 4 pins [form="♀ (female)"]
  R1_240 = Resistor [tolerance=±5% resistance=240 package=THT]
  R2_400 = Resistor [tolerance=±5% resistance=400 package=THT]
  RX--GP0--GP--GND = female pin header, 4 pins [form="♀ (female)"]
  GPIO_0 = female pin header, 2 pins [form="♀ (female)"]
  Rx_Tx = female pin header, 2 pins [form="♀ (female)"]
  Gnd_3_3V = female pin header, 2 pins [form="♀ (female)"]
  0_2 = female pin header, 2 pins [form="♀ (female)"]
  GPIO_1 = female pin header, 2 pins [form="♀ (female)"]
  R1 = Resistor [tolerance=±5% resistance=1k package=THT]

nets:
  N1: Power_plug1.GND, R2_400.Pin_0, RX--GP0--GP--GND.pin1, Gnd_3_3V.pin2
  N2: Power_plug1.VCC, Adj_Vout_Vin.IN
  N3: Adj_Vout_Vin.ADJ, R1_240.Pin_1, R2_400.Pin_1
  N4: Adj_Vout_Vin.OUT, VCC--RST--CH_P--TX.pin4, R1_240.Pin_0, Gnd_3_3V.pin1, R1.Pin_1
  N5: VCC--RST--CH_P--TX.pin1, Rx_Tx.pin1
  N6: VCC--RST--CH_P--TX.pin2, VCC--RST--CH_P--TX.pin3, GPIO_0.pin1, GPIO_1.pin2, R1.Pin_0
  N7: RX--GP0--GP--GND.pin2, 0_2.pin2, GPIO_1.pin1
  N8: RX--GP0--GP--GND.pin3, GPIO_0.pin2, 0_2.pin1
  N9: RX--GP0--GP--GND.pin4, Rx_Tx.pin2
