# Fritzing sketch id1614_RCSS_0 (saved by Fritzing 0.9.2b)

parts:
  Adafruit_HUZZAH_ESP8266_Breakout1 = Adafruit HUZZAH ESP8266 Breakout [part_number=2471]
  U6 = CustomPart
  CONN1 = USB connector [package=THT]
  LED1 = LED - 5mm [color="Red (633nm)" package="5 mm [THT]"]
  LED3 = LED - 5mm [color="Green (565nm)" package="5 mm [THT]"]
  LED4 = LED - 5mm [color="Yellow (595nm)" package="5 mm [THT]"]
  R2 = Resistor [tolerance=±5% resistance=200 package=THT]
  R3 = Resistor [tolerance=±5% resistance=200 package=THT]
  R1 = Resistor [tolerance=±5% resistance=200 package=THT]

nets:
  GND: Adafruit_HUZZAH_ESP8266_Breakout1.GND, U6.connector2, CONN1.GND, CONN1.chassis6, LED4.cathode
  N1: Adafruit_HUZZAH_ESP8266_Breakout1.#13, R1.Pin_1
  N2: Adafruit_HUZZAH_ESP8266_Breakout1.#12, R2.Pin_1
  N3: Adafruit_HUZZAH_ESP8266_Breakout1.#14, R3.Pin_1
  N4: Adafruit_HUZZAH_ESP8266_Breakout1.#5, U6.connector1
  N5: Adafruit_HUZZAH_ESP8266_Breakout1.3V, U6.connector3
  N6: Adafruit_HUZZAH_ESP8266_Breakout1.V+, CONN1.5V
  N7: LED1.anode, R3.Pin_0
  N8: LED3.anode, R1.Pin_0
  N9: LED4.anode, R2.Pin_0
