# Fritzing sketch id1615_temp_sensor_0 (saved by Fritzing 0.9.3b)
breadboards: 1

parts:
  Part1 = Arduino Uno (Rev3)
  T1 = LM35 Temperature Sensor [package="TO92 [THT]"]
  Espessif_Serial_Wifi_Modul_1 = ESP8266_Wifi_Modul [part_number=ESP8266]

nets:
  N1: Part1.A0, T1.Vout
  N2: Part1.D0/RX, Espessif_Serial_Wifi_Modul_1.connector2
  N3: Part1.D1/TX, Espessif_Serial_Wifi_Modul_1.connector1
  N4: Part1.3V3, Espessif_Serial_Wifi_Modul_1.connector3, Espessif_Serial_Wifi_Modul_1.connector7
  N5: Part1.5V, T1.+Vs
  GND: Part1.GND, T1.GND, Espessif_Serial_Wifi_Modul_1.connector0
