# Fritzing sketch id1617_esp8266_brekout_0 (saved by Fritzing 0.9.3b)
circuit board: 7cm x 3cm
breadboards: 1

parts:
  R3 = Resistor [tolerance=±5% resistance=10k package=THT]
  R4 = Resistor [tolerance=±5% resistance=10k package=THT]
  R5 = Resistor [tolerance=±5% resistance=10k package=THT]
  R2 = Resistor [tolerance=±5% resistance=10k package=THT]
  R1 = Resistor [tolerance=±5% resistance=10k package=THT]
  R7 = Resistor [tolerance=±5% resistance=470 package=THT]
  sleep = Resistor [tolerance=±5% resistance=470 package=THT]
  USB-TTL = fttl_uart_pins [form="♀ (female)"]
  RST = SWITCH-MOMENTARY-2 [package=tactile-pth]
  PRG = SWITCH-MOMENTARY-2 [package=tactile-pth]
  3V3 = Voltage Regulator [package=sot223]
  ESP8266 = ESP8266_module [part_number=ESP8266]
  C_PWR = Electrolytic Capacitor [capacitance=22µF voltage=10V package="100 mil [THT, electrolytic]"]
  C_PWR1 = Electrolytic Capacitor [capacitance=10µF voltage=10V package="100 mil [THT, electrolytic]"]

nets:
  N1: R3.Pin_0, ESP8266.connector4
  N2: R3.Pin_1, R5.Pin_1, R2.Pin_1, R1.Pin_1, 3V3.OUT, ESP8266.connector1, C_PWR.+
  N3: R4.Pin_0, USB-TTL.connector5, RST.1, PRG.1, 3V3.ADJ, ESP8266.connector6, C_PWR.-, C_PWR1.-
  N4: R4.Pin_1, ESP8266.connector8
  N5: R5.Pin_0, R7.Pin_0, USB-TTL.connector0, PRG.2
  N6: R2.Pin_0, ESP8266.connector5
  N7: R1.Pin_0, sleep.Pin_1, USB-TTL.connector4, RST.2, ESP8266.connector16
  N8: R7.Pin_1, ESP8266.connector2
  N9: sleep.Pin_0, ESP8266.connector12
  N10: USB-TTL.connector1, ESP8266.connector7
  N11: USB-TTL.connector2, ESP8266.connector0
  N12: USB-TTL.connector3, 3V3.IN, C_PWR1.+
