# Fritzing sketch id1618_ESP8266_A6_0 (saved by Fritzing 0.9.3b)
breadboards: 1

parts:
  A6_Module_Ver3 = IC, DIP package, 24 pins [chip_label="A6 GSM"]
  WeMos_D1_Mini1 = WeMos D1 Mini
  R1 = Resistor [tolerance=±5% resistance=2.2k package=THT]
  R2 = Resistor [tolerance=±5% resistance=2.2k package=THT]
  2N2222 = NPN-Transistor [package="TO92 [THT]"]
  2N2222_2 = NPN-Transistor [package="TO92 [THT]"]
  R3 = Resistor [tolerance=±5% resistance=220 package=THT]
  R4 = Resistor [tolerance=±5% resistance=220 package=THT]
  S1 = SPST Switch [package=switch-spst-smd-a]

nets:
  N1: A6_Module_Ver3.pin1, WeMos_D1_Mini1.5V, 2N2222_2.C, S1.S
  GND: A6_Module_Ver3.pin2, WeMos_D1_Mini1.G, R1.Pin_1, R2.Pin_1, 2N2222.E
  N2: A6_Module_Ver3.pin8, WeMos_D1_Mini1.D2
  N3: A6_Module_Ver3.pin9, WeMos_D1_Mini1.D1
  N4: A6_Module_Ver3.pin13, 2N2222_2.E
  N5: A6_Module_Ver3.pin19, 2N2222.C
  N6: WeMos_D1_Mini1.D7, R4.Pin_0
  N7: WeMos_D1_Mini1.D8, R3.Pin_0
  N8: R1.Pin_0, 2N2222_2.B, R3.Pin_1
  N9: R2.Pin_0, 2N2222.B, R4.Pin_1
  5V: S1.P
