# Fritzing sketch id1619_ESP8266_12_breakout_board_2layer_0 (saved by Fritzing 0.9.2b)
circuit board: 4cm x 2.9cm
breadboards: 1

parts:
  U1 = ESP8266_module [part_number=ESP8266]
  PRG = male pin header, 2 pins [form="♂ (male)"]
  TTL = female pin header, 6 pins [form="♀ (female)"]
  3V3 = Battery
  C1 = Electrolytic Capacitor [capacitance=0.22mF voltage=10V package="100 mil [THT, electrolytic]"]
  PRG_2 = Pushbutton [package="[THT]"]
  TTL3V3 = male pin header, 2 pins [form="♂ (male)"]
  CON2 = male pin header, 8 pins [form="♂ (male)"]
  CON1 = male pin header, 8 pins [form="♂ (male)"]
  RESET = Pushbutton [package="[THT]"]
  WK = Solder Jumper [package=sj_2s-no]
  R7 = Resistor [tolerance=±5% resistance=10k package="1206 [SMD]"]
  R10 = Resistor [tolerance=±5% resistance=10k package="1206 [SMD]"]
  R14 = Resistor [tolerance=±5% resistance=10k package="1206 [SMD]"]
  R13 = Resistor [tolerance=±5% resistance=10k package="1206 [SMD]"]
  R12 = Resistor [tolerance=±5% resistance=10k package="1206 [SMD]"]

nets:
  N1: U1.connector0, TTL.pin4, CON1.pin2
  N2: U1.connector1, 3V3.+, C1.+, TTL3V3.pin1, CON2.pin8, R7.Pin_1, R10.Pin_1, R13.Pin_1, R12.Pin_1
  N3: U1.connector2, PRG.pin1, PRG_2.Pin_3, PRG_2.Pin_4, CON1.pin5, R13.Pin_0
  N4: U1.connector4, CON1.pin6, R12.Pin_0
  N5: U1.connector5, CON2.pin3, R7.Pin_0
  N6: U1.connector6, PRG.pin2, TTL.pin1, 3V3.-, C1.-, PRG_2.Pin_1, PRG_2.Pin_2, CON1.pin8, RESET.Pin_1, RESET.Pin_2, R14.Pin_0
  N7: U1.connector7, TTL.pin5, CON1.pin1
  N8: U1.connector8, CON1.pin7, R14.Pin_1
  N9: U1.connector9, CON1.pin3
  N10: U1.connector10, CON1.pin4
  N11: U1.connector11, CON2.pin2
  N12: U1.connector12, CON2.pin4, WK.1
  N13: U1.connector13, CON2.pin5
  N14: U1.connector14, CON2.pin6
  N15: U1.connector15, CON2.pin7
  N16: U1.connector16, CON2.pin1, RESET.Pin_3, RESET.Pin_4, WK.2, R10.Pin_0
  N17: TTL.pin3, TTL3V3.pin2
