# Fritzing sketch id1620_ESP8266_12_breakout_board_2layer_1_0 (saved by Fritzing 0.9.2b)
circuit board: 3.4cm x 3.2cm
breadboards: 1

parts:
  ESP8266 = ESP8266_module [part_number=ESP8266]
  TTL = female pin header, 6 pins [form="♀ (female)"]
  C1 = Electrolytic Capacitor [capacitance=0.22mF voltage=10V package="100 mil [THT, electrolytic]"]
  TTL3V3 = male pin header, 2 pins [form="♂ (male)"]
  CON2 = male pin header, 8 pins [form="♂ (male)"]
  CON1 = male pin header, 8 pins [form="♂ (male)"]
  R7 = Resistor [tolerance=±5% resistance=10k package="1206 [SMD]"]
  R10 = Resistor [tolerance=±5% resistance=10k package="1206 [SMD]"]
  R14 = Resistor [tolerance=±5% resistance=10k package="1206 [SMD]"]
  R13 = Resistor [tolerance=±5% resistance=10k package="1206 [SMD]"]
  R12 = Resistor [tolerance=±5% resistance=10k package="1206 [SMD]"]
  PRG = SWITCH-MOMENTARY-2 [package=tactile_switch_smd]
  RST = SWITCH-MOMENTARY-2 [package=tactile_switch_smd]
  RST_2 = Solder Jumper [package=sj_2s-no]
  PRG_2 = Solder Jumper [package=sj_2s-no]
  WK = Solder Jumper [package=sj_2s-no]

nets (from the pcb view):
  N1: ESP8266.connector0, TTL.pin4, CON1.pin2
  N2: ESP8266.connector1, C1.+, TTL3V3.pin1, CON2.pin8, R7.Pin_1, R10.Pin_1, R13.Pin_1, R12.Pin_1
  N3: ESP8266.connector2, CON1.pin5, R13.Pin_0
  N4: ESP8266.connector4, CON1.pin6, R12.Pin_0, PRG.2, PRG_2.1
  N5: ESP8266.connector5, CON2.pin3, R7.Pin_0
  N6: ESP8266.connector6, TTL.pin1, C1.-, CON1.pin8, R14.Pin_0, PRG.1, RST.1
  N7: ESP8266.connector7, TTL.pin5, CON1.pin1
  N8: ESP8266.connector8, CON1.pin7, R14.Pin_1
  N9: ESP8266.connector9, CON1.pin3
  N10: ESP8266.connector10, CON1.pin4
  N11: ESP8266.connector11, CON2.pin2
  N12: ESP8266.connector12, CON2.pin4, WK.1
  N13: ESP8266.connector13, CON2.pin5
  N14: ESP8266.connector14, CON2.pin6
  N15: ESP8266.connector15, CON2.pin7
  N16: ESP8266.connector16, CON2.pin1, R10.Pin_0, RST.2, RST_2.1, WK.2
  N17: TTL.pin2, RST_2.2
  N18: TTL.pin3, TTL3V3.pin2
  N19: TTL.pin6, PRG_2.2
