# Fritzing sketch id1622_Drive_electronics (saved by Fritzing 0.9.3b)

parts:
  Componente1 = Arduino Mega 2560 (Rev3)
  Componente2 = Arduino Can-Bus Shield
  Componente3 = Arduino Mega 2560 (Rev3)  # not connected
  Componente4 = Arduino Can-Bus Shield
  Componente5 = Arduino Mega 2560 (Rev3)  # not connected
  Componente6 = Arduino Can-Bus Shield
  Componente7 = Arduino Mega 2560 (Rev3)  # not connected
  Componente8 = Arduino Can-Bus Shield
  U1 = 74AHC1G08 [package=sot23-5]
  U2 = 74AHC1G08 [package=sot23-5]
  R1 = Rotary Potentiometer (Large) [maximum_resistance=100kΩ package=THT]
  R2 = Rotary Potentiometer (Large) [maximum_resistance=100kΩ package=THT]
  U3 = RELAY [package=relay-jzc]
  U4 = RELAY [package=relay-jzc]
  U5 = HALL-EFFECT [package=sc70]
  U7 = HALL-EFFECT [package=sc70]
  M2 = DC Motor
  M3 = DC Motor
  Componente9 = EasyDriver_v44  # not connected
  Componente10 = EasyDriver_v44  # not connected
  Componente11 = EasyDriver_v44  # not connected
  Componente12 = EasyDriver_v44  # not connected

nets:
  N1: Componente1.D22, U3.COIL1
  N2: Componente1.D23, U4.COIL1
  N3: Componente2.CANH, Componente4.CANH, Componente6.CANH, Componente8.CANH
  N4: Componente2.CANL, Componente4.CANL, Componente6.CANL, Componente8.CANL
  N5: Componente2.A0, Componente4.A0, R1.wiper
  N6: Componente2.JOY-UP, Componente4.JOY-UP, R2.wiper
  N7: Componente2.CAN_INT, U5.OUT
  N8: Componente2.D3, U7.OUT
  N9: Componente2.SD_CS, M2.pin_1
  N10: Componente2.CAN_CS, M3.pin_1
  N11: Componente2.SCK, U1.B
  N12: Componente4.SCK, U2.B
  N13: Componente6.SCK, U1.A
  N14: Componente8.RS, U2.Y
  N15: U1.Y, U2.A

notes:
  WATCHDOG
  TRACTION
  BRAKING
  STEERING
  LOGIC ANDs
  Steer/Torque sensor
  Direction switches
