# Fritzing sketch id1622_ESP8266_12_breakout_board_2layer_V2_0 (saved by Fritzing 0.9.2b)
circuit board: 3.4cm x 3.2cm
breadboards: 1

parts:
  RST = SWITCH-MOMENTARY-2 [package=tactile_switch_smd]
  PRG = SWITCH-MOMENTARY-2 [package=tactile_switch_smd]
  PRG2 = Solder Jumper [package=sj_2s-no]
  RST2 = Solder Jumper [package=sj_2s-no]
  WK = Solder Jumper [package=sj_2s-no]
  TTL1 = female pin header, 6 pins [form="♀ (female)"]
  ESP8267 = ESP8266_module [part_number=ESP8266]
  R15 = Resistor [tolerance=±5% resistance=10k package="1206 [SMD]"]
  R16 = Resistor [tolerance=±5% resistance=10k package="1206 [SMD]"]
  R17 = Resistor [tolerance=±5% resistance=10k package="1206 [SMD]"]
  R18 = Resistor [tolerance=±5% resistance=10k package="1206 [SMD]"]
  R19 = Resistor [tolerance=±5% resistance=10k package="1206 [SMD]"]
  CON3 = male pin header, 8 pins [form="♂ (male)"]
  CON4 = male pin header, 8 pins [form="♂ (male)"]
  TTL3V3 = male pin header, 2 pins [form="♂ (male)"]
  C2 = Electrolytic Capacitor [capacitance=0.22mF voltage=10V package="100 mil [THT, electrolytic]"]

nets:
  N1: RST.1, PRG.1, TTL1.pin1, ESP8267.connector6, R15.Pin_0, CON3.pin8, C2.-
  N2: RST.2, RST2.1, WK.1, ESP8267.connector16, R16.Pin_0, CON4.pin1
  N3: PRG.2, PRG2.1, ESP8267.connector2, R18.Pin_0, CON3.pin5
  N4: PRG2.2, TTL1.pin6
  N5: RST2.2, TTL1.pin2
  N6: WK.2, ESP8267.connector12, CON4.pin4
  N7: TTL1.pin3, TTL3V3.pin2
  N8: TTL1.pin4, ESP8267.connector0, CON3.pin2
  N9: TTL1.pin5, ESP8267.connector7, CON3.pin1
  N10: ESP8267.connector1, R16.Pin_1, R17.Pin_1, R18.Pin_1, R19.Pin_1, CON4.pin8, TTL3V3.pin1, C2.+
  N11: ESP8267.connector4, R17.Pin_0, CON3.pin6
  N12: ESP8267.connector5, R19.Pin_0, CON4.pin3
  N13: ESP8267.connector8, R15.Pin_1, CON3.pin7
  N14: ESP8267.connector9, CON3.pin3
  N15: ESP8267.connector10, CON3.pin4
  N16: ESP8267.connector11, CON4.pin2
  N17: ESP8267.connector13, CON4.pin5
  N18: ESP8267.connector14, CON4.pin6
  N19: ESP8267.connector15, CON4.pin7
