# Fritzing sketch id1624_IR_Transmitter_0 (saved by Fritzing 0.9.2b)

parts:
  U1 = NodeMCU
  Q1 = NPN-Transistor [package="TO92 [THT]"]
  LED1 = smd LED [color="Infrared (940nm)" package="0805 [SMD]"]

nets:
  N1: U1.connector2, U1.connector10, Q1.B
  N2: U1.connector5, LED1.anode
  N3: U1.connector33, Q1.E
  N4: Q1.C, LED1.cathode
