# Fritzing sketch id1625_esp8266_module_0 (saved by Fritzing 0.9.2b)
circuit board: 3.70989cm x 2.6172cm
breadboards: 1

parts:
  ESP-01 = ESP8266_module [part_number=ESP8266]
  JP3 = header-1x4
  C1 = Capacitor Polarized [package=cpol-radial-100uf-25v]
  PRG = Momentary Switch [package=tactile-pth]
  RST = Momentary Switch [package=tactile-pth]
  R1 = Resistor [tolerance=±5% resistance=10k package=THT]
  R2 = Resistor [tolerance=±5% resistance=10k package=THT]
  R3 = Resistor [tolerance=±5% resistance=10k package=THT]
  GPIO = header-1x2
  RX(5V) = header-1x1
  R4 = Resistor [tolerance=±5% resistance=10k package=THT]
  R5 = Resistor [tolerance=±5% resistance=22k package=THT]
  GND = header-1x1

nets:
  N1: ESP-01.connector0, JP3.connector1, R4.Pin_0, R5.Pin_1
  N2: ESP-01.connector1, JP3.connector0, C1.+, R1.Pin_1, R2.Pin_1, R3.Pin_1
  N3: ESP-01.connector2, PRG.3, PRG.4, R1.Pin_0, GPIO.connector0
  N4: ESP-01.connector3, RST.3, RST.4, R2.Pin_0
  N5: ESP-01.connector4, GPIO.connector1
  N6: ESP-01.connector5, R3.Pin_0
  N7: ESP-01.connector6, JP3.connector3, C1.-, PRG.1, PRG.2, RST.1, RST.2, R5.Pin_0, GND.connector0
  N8: ESP-01.connector7, JP3.connector2
  N9: RX(5V).connector0, R4.Pin_1

notes:
  3.3V
  GND
  RX
  TX
  GPIO_0
  GPIO_2
  0
  2
  TX CH_PD RST VCC
  GND G2 G0 RX
