# Fritzing sketch id1626_Plant_Monitor_V1.fz_0 (saved by Fritzing 0.9.3b)
breadboards: 1

parts:
  U1 = ESP8266 WiFi Module [part_number=ESP8266]
  Part1 = BME280 Breakout
  Part2 = Soil Moisture Sensor

nets:
  N1: U1.IO2, Part2.SIG
  N2: U1.CLK, Part1.SCK/SCL
  N3: U1.D1, Part1.SDI/SDA
  3.3V: U1.3.3V#11, Part1.3.3V, Part2.VCC
  GND: U1.GND#12, Part1.GND, Part2.GND
