# Fritzing sketch id1627_esp8266_programming_jig_0 (saved by Fritzing 0.9.2b)
circuit board: 3.63113cm x 3.59349cm
breadboards: 1

parts:
  U1 = ESP8266_module [part_number=ESP8266]
  S1 = Toggle Switch [package=THT]
  S2_(RST) = Pushbutton [package="[THT]"]
  J1 = male pin header, 3 pins [form="♂ (male)"]
  J2 = double row male pin header, 14 pins [form="♂ (male)"]
  R1 = Resistor [tolerance=±5% resistance=220 package=THT]
  FTDI = FTDI_header [form="♂ (male)"]

nets:
  N1: U1.connector0, FTDI.connector2
  3.3V: U1.connector1, J2.pin12, J2.pin14, R1.Pin_1, FTDI.connector3
  N2: U1.connector2, S1.COM
  N3: U1.connector3, J1.pin3
  N4: U1.connector4, J2.pin1
  N5: U1.connector5, J1.pin1
  GND: U1.connector6, S1.L2, S2_(RST).Pin_1, S2_(RST).Pin_2, J2.pin11, J2.pin13, FTDI.connector5
  N6: U1.connector7, FTDI.connector1
  N7: S1.L1, J2.pin2
  N8: S2_(RST).Pin_3, S2_(RST).Pin_4, J1.pin2, R1.Pin_0
