# Fritzing sketch id1628_Programming_ESP_0 (saved by Fritzing 0.9.3b)
breadboards: 1

parts:
  ESP8266_WiFi_Module = SparkFun ESP8266 Thing
  Arduino_Uno = Arduino Uno (Rev3)

nets:
  GND: ESP8266_WiFi_Module.GND, ESP8266_WiFi_Module.GPIO0, Arduino_Uno.GND
  VCC: ESP8266_WiFi_Module.VCC, Arduino_Uno.3V3
  N1: ESP8266_WiFi_Module.U0TXO, Arduino_Uno.D1/TX
  N2: ESP8266_WiFi_Module.U0RXI, Arduino_Uno.D0/RX
