# Fritzing sketch id1629_RemoteSchema_0 (saved by Fritzing 0.9.3b)
breadboards: 1

parts:
  U1 = NodeMCU
  Grove1 = Grove Infrared Emitter
  U4 = RF-LINK_TX [package=rf-link_tx]
  U5 = RF-LINK_RX [package=rf-link_rx]
  Grove2 = Grove Infrared Receiver

nets:
  N1: U1.connector1, U5.DATA
  N2: U1.connector2, U4.DATA
  N3: U1.connector7, Grove2.RX
  N4: U1.connector8, Grove1.TX
  VCC: U1.connector15, Grove1.VCC, U4.+5V, U5.+5V, Grove2.VCC
  GND: U1.connector16, Grove1.GND, U4.GND, U5.GND, Grove2.GND
