# Fritzing sketch id162_555_timer_led_0 (saved by Fritzing 0.9.2b)
breadboards: 1

parts:
  U1 = 555 Timer [package="DIP8 [THT]"]
  C1 = Capacitor Polarized [package=panasonic_c]
  R1 = Resistor [tolerance=±5% resistance=220 package="2010 [SMD]"]
  R2 = Resistor [tolerance=±5% resistance=220 package="0805 [SMD]"]
  LED1 = LED - 3mm [color="Red (633nm)" package="3 mm [THT]"]
  R3 = Resistor [tolerance=±5% resistance=220 package="2010 [SMD]"]
  VCC1 = Battery block 9V

nets:
  N1: U1.Ground, C1.+, VCC1.-, VCC1.+
  N2: U1.Trigger, U1.Threshold, R1.Pin_1, R3.Pin_1
  N3: U1.Output, C1.-
  N4: U1.Reset, U1.Vcc_Supply_Voltage, R2.Pin_0, LED1.cathode
  N5: U1.Discharge, R2.Pin_1, R3.Pin_0
  N6: R1.Pin_0, LED1.anode
