# Fritzing sketch id1630_esp8266_test_0 (saved by Fritzing 0.9.2b)

parts:
  ESP8266 = ESP8266_module_2 [part_number=ESP8266]
  U1 = Voltage Regulator [package=to220-adj]
  Part1 = FTDI Basic Programmer

nets:
  N1: ESP8266.connector0, Part1.RXI
  N2: ESP8266.connector1, ESP8266.connector5, U1.OUT
  N3: ESP8266.connector6, U1.ADJ, Part1.GND
  N4: ESP8266.connector7, Part1.TXO
  N5: U1.IN, Part1.POWER
