# Fritzing sketch id1632_ESP8266_starter_0 (saved by Fritzing 0.9.2b)
breadboards: 1

parts:
  U1 = ESP8266_module [part_number=ESP8266]
  Part1 = Arduino Uno (Rev3)
  U2 = V_REG_LD1117VXX [package=78xxl]
  Part2 = FTDI Basic Programmer

nets:
  N1: U1.connector0, Part2.TXO
  N2: U1.connector1, U1.connector5, U2.OUT
  GND: U1.connector6, Part1.GND, U2.GND
  N3: U1.connector7, Part2.RXI
  N4: Part1.5V, U2.IN
