# Fritzing sketch id1633_esp8266v1_0 (saved by Fritzing 0.9.3b)
breadboards: 1

parts:
  U1 = ESP8266_module [part_number=ESP8266]
  Part1 = FTDI Basic Programmer
  S1 = Toggle Switch [package=THT]

nets:
  N1: U1.connector0, Part1.TXO
  N2: U1.connector1, S1.COM
  N3: U1.connector6, Part1.GND
  N4: U1.connector7, Part1.RXI
  N5: Part1.POWER, S1.L1

notes:
  Wire colors are subjective and are not part of the actual set. Colors are from Fritzing, not the kit. Except for what is used to connect to FTDI device. [Kit refers to author's own kit of parts and jumpers.]
