# Fritzing sketch id1635_DryerAlarm (saved by Fritzing 0.9.3b)
breadboards: 1

parts:
  Part1 = Arduino Yun
  S1 = Pushbutton [package="[THT]"]
  LED1 = LED - 5mm [color="Red (633nm)" package="5 mm [THT]"]  # not connected
  IC1 = IC, DIP package, 6 pins [chip_label=2125]
  R1 = Resistor [tolerance=±5% resistance=10k package=THT]

nets:
  N1: Part1.D2, S1.Pin_3, S1.Pin_4, R1.Pin_1
  N2: Part1.D3_PWM, IC1.pin2
  N3: Part1.D4, IC1.pin5
  N4: Part1.5V, S1.Pin_1, S1.Pin_2, IC1.pin3
  N5: Part1.GND, IC1.pin1, IC1.pin6, R1.Pin_0
