# Fritzing sketch id1637_ESP8266_07_with_PowerSupply_and_SIM_V03_0 (saved by Fritzing 0.9.3b)
circuit board: 3.9cm x 2.81737cm
perfboards: 1

parts:
  RST = SWITCH-MOMENTARY-2 [package=tactile_switch_smd]
  PRG = SWITCH-MOMENTARY-2 [package=tactile_switch_smd]
  Serial = female pin header, 6 pins [form="♀ (female)"]
  R6 = Resistor [tolerance=±5% resistance=10k package="1206 [SMD]"]
  R2 = Resistor [tolerance=±5% resistance=10k package="1206 [SMD]"]
  R3 = Resistor [tolerance=±5% resistance=10k package="1206 [SMD]"]
  R4 = Resistor [tolerance=±5% resistance=10k package="1206 [SMD]"]
  R5 = Resistor [tolerance=±5% resistance=10k package="1206 [SMD]"]
  CON1 = male pin header, 8 pins [form="♂ (male)"]
  C1 = Electrolytic Capacitor [capacitance=0.22mF voltage=10V package="100 mil [THT, electrolytic]"]
  3V3 = male pin header, 3 pins [form="♂ (male)"]
  7-36V = male pin header, 3 pins [form="♂ (male)"]
  ESP_8266 = ESP8266 WiFi Module [part_number=ESP8266]
  R1 = Resistor [tolerance=±5% resistance=10k package="1206 [SMD]"]
  RST2 = Solder Jumper [package=sj_2s-no]
  PRG2 = Solder Jumper [package=sj_2s-no]
  WK = Solder Jumper [package=sj_2s-no]
  LED1 = LED - 3mm [color="Red (633nm)" package="3 mm [THT]"]
  CON2 = male pin header, 8 pins [form="♂ (male)"]
  GPRS = SIM800L [package=THT]
  ESP8266 = ESP8266_module [part_number=ESP8266]

nets:
  GND: RST.1, PRG.1, Serial.pin1, R6.Pin_0, C1.-, 3V3.pin2, 7-36V.pin2, ESP_8266.GND, LED1.cathode, CON2.pin8, GPRS.GND, ESP8266.connector6
  RST: RST.2, R2.Pin_0, CON1.pin1, ESP_8266.REST, RST2.1, WK.1, ESP8266.connector16
  GPIO00: PRG.2, R4.Pin_0, ESP_8266.GPIO_0, PRG2.1, CON2.pin5, ESP8266.connector2
  RTS: Serial.pin2, RST2.2
  3V3: Serial.pin3, R2.Pin_1, R3.Pin_1, R4.Pin_1, R5.Pin_1, CON1.pin8, C1.+, 3V3.pin1, 7-36V.pin1, ESP_8266.VCC, R1.Pin_1, LED1.anode, ESP8266.connector1
  RXD: Serial.pin4, ESP_8266.RXD, CON2.pin2, ESP8266.connector0
  TXD: Serial.pin5, ESP_8266.TXD, CON2.pin1, ESP8266.connector7
  DTR: Serial.pin6, PRG2.2
  N1: R6.Pin_1, ESP_8266.GPIO_15, CON2.pin7, ESP8266.connector8
  GPIO02: R3.Pin_0, ESP_8266.GPIO_2, CON2.pin6, ESP8266.connector4
  N2: R5.Pin_0, CON1.pin3, ESP_8266.CH_PD, ESP8266.connector5
  ADC: CON1.pin2, ESP_8266.ADC_0, ESP8266.connector11
  GPIO16: CON1.pin4, ESP_8266.GPIO_16, WK.2, ESP8266.connector12
  GPIO14: CON1.pin5, ESP_8266.GPIO_14, GPRS.SIM_RXD, ESP8266.connector13
  GPIO12: CON1.pin6, ESP_8266.GPIO_12, R1.Pin_0, ESP8266.connector14
  GPIO13: CON1.pin7, ESP_8266.GPIO_13, GPRS.SIM_TXD, ESP8266.connector15
  VIN: 3V3.pin3, 7-36V.pin3, GPRS.5V
  GPI004: ESP_8266.GPIO_4, CON2.pin3, GPRS.RST, ESP8266.connector9
  GPIO05: ESP_8266.GPIO_5, CON2.pin4, ESP8266.connector10

notes:
  EspIoT V03
  RXD
  TXD
  RTS
  DTR
  GND
  3,3V
  ESP-MQTT-SD0.1
