# Fritzing sketch id1638_ESPrDeveloper_WiFi_RC_0 (saved by Fritzing 0.9.3b)
breadboards: 2

parts:
  U1 = TA7291P  # not connected
  U2 = TA7291P  # not connected
  Adafruit_HUZZAH_ESP8266_Breakout1 = Adafruit HUZZAH ESP8266 Breakout [part_number=2471]
  M1 = DC Motor
  M2 = DC Motor  # not connected

nets:
  N1: Adafruit_HUZZAH_ESP8266_Breakout1.#14, M1.pin_2
