# Fritzing sketch id1639_DS18B20_LCD (saved by Fritzing 0.9.3b)
circuit board: 8.46667cm x 5.64444cm
breadboards: 1

parts:
  LCD1 = LCD screen  # not connected
  Part1 = Arduino Uno (Rev3)
  IIC1 = iic_converter
  DS1 = DS18B20 1-Wire Temperature Sensor [part_number=DS18B20]
  R1 = Resistor [tolerance=±5% resistance=4.7k package=THT]

nets:
  N1: Part1.A4/SDA, IIC1.connector17
  N2: Part1.A5/SCL, IIC1.connector16
  GND: Part1.GND, IIC1.connector19, DS1.GND
  N3: Part1.D3_PWM, DS1.DQ, R1.Pin_0
  5V: Part1.5V, IIC1.connector18, DS1.VDD, R1.Pin_1
