# Fritzing sketch id163_555PWM_0 (saved by Fritzing 0.7.7b)
breadboards: 1

parts:
  R1 = Trimmer Potentiometer [maximum_resistance=10kΩ package=THT]
  Q1 = Basic FET N-Channel [package="TO220 [THT]"]
  D1 = Rectifier Diode [part_number=1N4001 package="300 mil [THT]"]
  D2 = Rectifier Diode [part_number=1N4001 package="300 mil [THT]"]
  D3 = Rectifier Diode [part_number=1N4001 package="300 mil [THT]"]
  C1 = Tantalum Capacitor [capacitance=10pF package="100 mil [THT, tantalum]"]
  C2 = Tantalum Capacitor [capacitance=10pF package="100 mil [THT, tantalum]"]
  M1 = DC Motor
  VCC1 = Battery
  U1 = 555 Timer [package="DIP8 [THT]"]
  R3 = Resistor [tolerance=±5% resistance=1k package=THT]
  R2 = Resistor [tolerance=±5% resistance=1k package=THT]

nets:
  N1: R1.leg1, D1.anode
  N2: R1.wiper, C1.+, U1.Trigger, U1.Threshold
  N3: R1.leg2, D2.cathode
  N4: Q1.gate, R2.Pin_0
  N5: Q1.drain, D3.anode, M1.pin_1
  N6: Q1.source, C1.-, C2.-, VCC1.-, U1.Ground
  N7: D1.cathode, D2.anode, R3.Pin_0
  N8: D3.cathode, M1.pin_2, VCC1.+, U1.Reset, U1.Vcc_Supply_Voltage, R3.Pin_1
  N9: C2.+, U1.Control_Voltage
  N10: U1.Output, R2.Pin_1

notes:
  RFP30N06LE
  1N5402
  1k
  10pF
  BATT
  -
  +
  LOAD
  trimpot
  555
  v. 0.1
  555PWM
  by buildchimp
