# Fritzing sketch id1640_esquemaalto_falante_0 (saved by Fritzing 0.9.2b)
breadboards: 1

parts:
  Componente1 = Arduino Uno (Rev3)
  U1 = XBee
  SPKR1 = Loudspeaker
  R1 = Resistor [tolerance=±5% resistance=100 package="2010 [SMD]"]
  Q1 = TRANSISTOR_NPN [package=to-92-ammo]
  U2 = microSD Socket [package=usd-socket-pp]

nets:
  N1: Componente1.D10_PWM/SS, U2.RSV
  N2: Componente1.D11_PWM/MOSI, U2.DI
  N3: Componente1.D12/MISO, U2.DO
  N4: Componente1.D13/SCK, U2.SCK
  GND: Componente1.GND, U1.GND, SPKR1.pin2, U2.GND
  N5: Componente1.D0/RX, U1.pin2
  N6: Componente1.D1/TX, U1.pin3
  N7: Componente1.D6_PWM, R1.Pin_0
  3V3: Componente1.3V3, U1.VCC
  5V: Componente1.5V, U2.VCC
  N8: SPKR1.pin1, Q1.E
  N9: R1.Pin_1, Q1.B
