# Fritzing sketch id1641_Esquema_Frizing_Robot_DYOR_Vintage_0 (saved by Fritzing 0.9.3b)

parts:
  Arduino_Nano_+_Shield2 = arduino_nano_v3.0_io_expansion
  hc-sr1_(ultrasonido)2 = HC-SR04
  Matriz_LEDs_8x10 = LED_matrix_8x8
  VCC2 = Battery block 9V  # not connected
  Seguidor_linia2 = TCRT5000_Line_Tracker
  Servo_rueda1 = servo360
  Modulo_bluetooth2 = Bluetooth HC-06
  Servo_rueda2 = servo360
  Servo_rueda3 = servo360
  Zumbador2 = KY-006
  Servo_rueda4 = servo360

nets:
  N1: Arduino_Nano_+_Shield2.connector20, Modulo_bluetooth2.connector2
  N2: Arduino_Nano_+_Shield2.connector21, Servo_rueda2.connector3
  N3: Arduino_Nano_+_Shield2.connector22, Modulo_bluetooth2.connector3
  N4: Arduino_Nano_+_Shield2.connector23, Servo_rueda3.connector3
  N5: Arduino_Nano_+_Shield2.connector24, Servo_rueda1.connector3
  N6: Arduino_Nano_+_Shield2.connector25, hc-sr1_(ultrasonido)2.connector3
  N7: Arduino_Nano_+_Shield2.connector26, Zumbador2.connector0
  N8: Arduino_Nano_+_Shield2.connector27, Servo_rueda4.connector3
  N9: Arduino_Nano_+_Shield2.connector28, Matriz_LEDs_8x10.connector3
  N10: Arduino_Nano_+_Shield2.connector29, Matriz_LEDs_8x10.connector5
  N11: Arduino_Nano_+_Shield2.connector30, Matriz_LEDs_8x10.connector2
  N12: Arduino_Nano_+_Shield2.connector42, Seguidor_linia2.connector3
  N13: Arduino_Nano_+_Shield2.connector52, Modulo_bluetooth2.connector1
  N14: Arduino_Nano_+_Shield2.connector53, Servo_rueda2.connector1
  N15: Arduino_Nano_+_Shield2.connector55, Servo_rueda3.connector1
  N16: Arduino_Nano_+_Shield2.connector56, Servo_rueda1.connector1
  N17: Arduino_Nano_+_Shield2.connector58, Zumbador2.connector2
  N18: Arduino_Nano_+_Shield2.connector59, Servo_rueda4.connector1
  N19: Arduino_Nano_+_Shield2.connector62, Matriz_LEDs_8x10.connector1
  N20: Arduino_Nano_+_Shield2.connector63, hc-sr1_(ultrasonido)2.connector4
  N21: Arduino_Nano_+_Shield2.connector68, Seguidor_linia2.connector1
  N22: Arduino_Nano_+_Shield2.connector81, Modulo_bluetooth2.connector0
  N23: Arduino_Nano_+_Shield2.connector82, Servo_rueda2.connector2
  N24: Arduino_Nano_+_Shield2.connector84, Servo_rueda3.connector2
  N25: Arduino_Nano_+_Shield2.connector85, Servo_rueda1.connector2
  N26: Arduino_Nano_+_Shield2.connector87, Zumbador2.connector3
  N27: Arduino_Nano_+_Shield2.connector88, Servo_rueda4.connector2
  N28: Arduino_Nano_+_Shield2.connector91, Matriz_LEDs_8x10.connector0
  N29: Arduino_Nano_+_Shield2.connector93, hc-sr1_(ultrasonido)2.connector1
  N30: Arduino_Nano_+_Shield2.connector97, Seguidor_linia2.connector0
  N31: Arduino_Nano_+_Shield2.connector111, hc-sr1_(ultrasonido)2.connector2
