# Fritzing sketch id1642_Esquema_para_un_servomotor_0 (saved by Fritzing 0.9.3b)
breadboards: 1

parts:
  Componente1 = Arduino Uno (Rev3)
  R1 = Rotary Potentiometer (Small) [maximum_resistance=100kΩ package=THT]
  J1 = Basic Servo

nets:
  N1: Componente1.A0, R1.wiper
  N2: Componente1.D2, J1.pulse
  5V: Componente1.5V, R1.leg1, J1.vcc
  GND: Componente1.GND, R1.leg2, J1.gnd
