# Fritzing sketch id1643_Practica2_0 (saved by Fritzing 0.9.3b)
breadboards: 1

parts:
  Componente1 = Arduino Uno (Rev3)
  LED1 = smd LED [color="Green (570nm)" package="0603 [SMD]"]
  LED2 = smd LED [color="Yellow (595nm)" package="0603 [SMD]"]
  LED3 = smd LED [color="Red (633nm)" package="0603 [SMD]"]
  R1 = Resistor [tolerance=±5% resistance=220 package="1206 [SMD]"]
  R2 = Resistor [tolerance=±5% resistance=220 package="1206 [SMD]"]
  R3 = Resistor [tolerance=±5% resistance=220 package="1206 [SMD]"]
  U1 = LCD-16X2 [package=lcd-16x2]  # not connected
  R4 = Trimmer Potentiometer [maximum_resistance=10kΩ package=THT]
  Componente2 = Barometric Pressure Sensor - BMP180 Breakout (GY-68)
  RHT1 = Humidity and Temperature Sensor RHT03

nets (from the breadboard view):
  N1: Componente1.A0, Componente2.SDA
  N2: Componente1.A1, Componente2.SCL
  N3: Componente1.D0/RX, RHT1.Data-signal
  N4: Componente1.D3_PWM, LED1.anode
  N5: Componente1.D4, LED2.anode
  N6: Componente1.D5_PWM, LED3.anode
  VCC: Componente1.5V, R4.leg1, Componente2.VCC, RHT1.Vcc
  GND: Componente1.GND, R1.Pin_1, R2.Pin_1, R3.Pin_1, R4.leg2, Componente2.GND, RHT1.GND_1
  N7: LED1.cathode, R1.Pin_0
  N8: LED2.cathode, R2.Pin_0
  N9: LED3.cathode, R3.Pin_0

notes:
  Pines LCD
  1. VSS
  2. VDD
  3. VO
  4. RS
  5. RW
  6. E
  7. D0
  8. D1
  9. D2
  10. D3
  11. D4
  12. D5
  13. D6
  14. D7
  15. A
  16. K
  Sensor de Humedad DHT11
  Sensor de presión BMP180
