# Fritzing sketch id1644_TestEth_0 (saved by Fritzing 0.9.3b)
breadboards: 1

parts:
  Componente2 = Arduino Uno (Rev3)
  LCD2 = LCD screen
  R2 = Trimmer Potentiometer [maximum_resistance=10kΩ package=THT]
  U1 = 74HC595 [package="DIP16 [THT]"]
  R3 = Resistor [tolerance=±5% resistance=10k package=THT]
  R4 = Resistor [tolerance=±5% resistance=10k package=THT]
  R5 = Resistor [tolerance=±5% resistance=10k package=THT]
  R6 = Resistor [tolerance=±5% resistance=10k package=THT]
  R7 = Resistor [tolerance=±5% resistance=10k package=THT]
  R8 = Resistor [tolerance=±5% resistance=10k package=THT]
  R9 = Resistor [tolerance=±5% resistance=10k package=THT]
  R10 = Resistor [tolerance=±5% resistance=10k package=THT]
  U2 = RJ45 Jack [package=rj45-8]
  U3 = RJ45 Jack [package=rj45-8]
  R11 = Resistor [tolerance=±5% resistance=10k package=THT]
  R12 = Resistor [tolerance=±5% resistance=10k package=THT]
  R14 = Resistor [tolerance=±5% resistance=10k package=THT]
  R16 = Resistor [tolerance=±5% resistance=10k package=THT]
  R17 = Resistor [tolerance=±5% resistance=10k package=THT]
  R19 = Resistor [tolerance=±5% resistance=10k package=THT]
  R20 = Resistor [tolerance=±5% resistance=10k package=THT]
  R21 = Resistor [tolerance=±5% resistance=10k package=THT]

nets:
  N1: Componente2.A0, U3.4, R21.Pin_0
  N2: Componente2.A1, U3.3, R20.Pin_0
  N3: Componente2.A2, U3.2, R11.Pin_0
  N4: Componente2.A3, U3.1, R17.Pin_0
  N5: Componente2.A4/SDA, U3.8, R16.Pin_0
  N6: Componente2.A5/SCL, U3.7, R12.Pin_0
  N7: Componente2.D8, LCD2.DB6
  N8: Componente2.D9_PWM, LCD2.DB7
  N9: Componente2.D11_PWM/MOSI, U1.SH_CP
  N10: Componente2.D12/MISO, U1.ST_CP
  N11: Componente2.D13/SCK, U1.DS
  N12: Componente2.D2, U3.5, R19.Pin_0
  N13: Componente2.D3_PWM, R14.Pin_0
  N14: Componente2.D4, LCD2.RS
  N15: Componente2.D5_PWM, LCD2.E
  N16: Componente2.D6_PWM, LCD2.DB4
  N17: Componente2.D7, LCD2.DB5
  5V: Componente2.5V, LCD2.VDD, LCD2.LED+, R2.leg2, U1.MR, U1.VCC
  GND: Componente2.GND, LCD2.VSS, LCD2.R/W, LCD2.LED-, R2.leg1, U1.OE, R3.Pin_1, R9.Pin_1, R16.Pin_1, R21.Pin_1
  N18: LCD2.V0, R2.wiper
  N19: U1.Q1, R4.Pin_0, U2.3
  N20: U1.Q2, R5.Pin_0, U2.2
  N21: U1.Q3, R8.Pin_0, U2.1
  N22: U1.Q4, R7.Pin_0, U2.8
  N23: U1.Q5, R6.Pin_0, U2.7
  N24: U1.Q6, R10.Pin_0, U2.6
  N25: U1.Q7, R9.Pin_0, U2.5
  N26: U1.Q0, R3.Pin_0, U2.4
  N27: R11.Pin_1, R19.Pin_1
