# Fritzing sketch id1645_tester_0 (saved by Fritzing 0.9.0b)
circuit board: 3.73457cm x 4.21016cm
breadboards: 1

parts:
  U1 = RJ45 Jack [package=rj45-8]
  LED1 = LEDs [package=led10mm]
  LED2 = LEDs [package=led10mm]
  LED3 = LEDs [package=led10mm]
  LED4 = LEDs [package=led10mm]

nets:
  N1: U1.1, LED1.C
  N2: U1.2, LED2.C
  N3: U1.3, LED3.C
  N4: U1.4, LED4.C
  N5: U1.5, LED4.A
  N6: U1.6, LED3.A
  N7: U1.7, LED2.A
  N8: U1.8, LED1.A

notes:
  Ethernet Tester
  V0.0.01
  Part A
