# Fritzing sketch id1646_tester_part_B_0 (saved by Fritzing 0.9.0b)
circuit board: 3.62442cm x 3.24924cm
breadboards: 1

parts:
  U1 = RJ45 Jack [package=rj45-8]
  IC1 = Voltage Regulator [package=to-220-alt]
  J1 = Power Jack [package=power_jack_combo]

nets:
  N1: U1.1, U1.2, U1.3, U1.4, IC1.OUT
  GND: U1.5, U1.6, U1.7, U1.8, IC1.GND, J1.GND
  N2: IC1.IN, J1.PWR

notes:
  Ethernet tester part B
  V0.0.1
