# Fritzing sketch id1647_Electric_Vehicle_prototype1_0 (saved by Fritzing 0.9.2b)
breadboards: 2

parts:
  Part1 = Arduino Uno (Rev3)
  R1 = Rotary Potentiometer (Small) [maximum_resistance=100kΩ package=THT]
  R2 = Rotary Potentiometer (Small) [maximum_resistance=100kΩ package=THT]
  M1 = DC Motor
  LCD1 = LCD screen
  U1 = ENCODER-QUADRATURE [package=encoder-16mm-quad]
  U2 = ENCODER-QUADRATURE [package=encoder-16mm-quad]

nets:
  N1: Part1.A1, R1.wiper
  N2: Part1.A2, R2.wiper
  N3: Part1.D8, LCD1.DB6
  N4: Part1.D9_PWM, LCD1.DB5
  N5: Part1.D10_PWM/SS, LCD1.DB4
  N6: Part1.D11_PWM/MOSI, LCD1.E
  N7: Part1.D12/MISO, LCD1.RS
  N8: Part1.D2, M1.pin_1
  N9: Part1.D3_PWM, M1.pin_2
  N10: Part1.D5_PWM, U2.C
  N11: Part1.D6_PWM, U1.C
  N12: Part1.D7, LCD1.DB7
  5V: Part1.5V, R1.leg1, R2.leg1, LCD1.VDD, U1.A, U2.A
  GND: Part1.GND, R1.leg2, R2.leg2, LCD1.VSS, LCD1.V0, LCD1.R/W, U1.B, U2.B
