# Fritzing sketch id1648_FriztingTest_0 (saved by Fritzing 0.9.3b)
breadboards: 1

parts:
  Onderdeel1 = Arduino Uno (Rev3) - ICSP
  LED1 = smd LED [color="Red (633nm)" package="0805 [SMD]"]
  hc-sr1 = hc-sr04
  R1 = Resistor [tolerance=±5% resistance=330 package="2512 [SMD]"]
  S1 = SWITCH-MOMENTARY-2 [package=tactile-pth]
  R2 = Resistor [tolerance=±5% resistance=330 package="2512 [SMD]"]

nets:
  N1: Onderdeel1.D12/MISO, hc-sr1.Echo
  N2: Onderdeel1.D13/SCK, hc-sr1.Trig
  N3: Onderdeel1.D5_PWM, LED1.anode
  5V: Onderdeel1.5V, hc-sr1.VCC
  GND: Onderdeel1.GND, hc-sr1.GND, R1.Pin_0, R2.Pin_0
  N4: LED1.cathode, R1.Pin_1
  N5: S1.2, R2.Pin_1
