# Fritzing sketch id1649_Untitled_Sketch_0 (saved by Fritzing 0.9.0b)
breadboards: 2

parts:
  U1 = RF-LINK_TX [package=rf-link_tx]  # not connected
  U2 = RF-LINK_RX [package=rf-link_rx]
  Part1 = Arduino Uno (Rev3)  # not connected
  Part2 = Arduino Uno (Rev3)

nets:
  +5V: U2.+5V, Part2.5V
