# Fritzing sketch id164_5_volt_power_suply (saved by Fritzing 0.3.8b)
breadboards: 1

parts:
  U1 = Voltage Regulator - 5V [package="TO220 [THT]"]
  Power_plug1 = Power plug
  C3 = Electrolytic Capacitor [package=THT]
  C5 = Electrolytic Capacitor [package=THT]
  J1 = Screw terminal [package=THT]

nets:
  N1: U1.input_voltage, Power_plug1.VCC, C5.+
  GND: U1.GND, Power_plug1.GND, C3.-, C5.-, J1.pin1
  N2: U1.output_voltage, C3.+, J1.pin2
