# Fritzing sketch id164_Untitled_Sketch_0 (saved by Fritzing 0.9.3b)
circuit board: 4.10192cm x 1.81013cm
breadboards: 1

parts:
  Input = Power plug [part_number="DC Input"]
  LM7805_IC = Voltage Regulator [package=to-220-alt]
  part = Ceramic Capacitor [capacitance=47µF voltage=6.3V package="100 mil [THT, multilayer]"]
  5V_Output = Screw terminal - 2 pins [package=THT]
  LED = smd LED [color="Red (633nm)" package="1206 [SMD]"]
  part_2 = Electrolytic Capacitor [capacitance=0.22mF voltage=35V package="100 mil [THT, electrolytic]"]

nets:
  GND: Input.GND, LM7805_IC.GND, part.1, 5V_Output.pin2, LED.cathode, part_2.-
  N1: Input.VCC, LM7805_IC.IN, part_2.+
  N2: LM7805_IC.OUT, part.0, 5V_Output.pin1, LED.anode
