# Fritzing sketch id1650_EstruturaBluetooth_0 (saved by Fritzing 0.9.2b)
breadboards: 1

parts:
  Componente1 = Arduino Uno (Rev3)
  LED1 = LED - 5mm [color="Red (633nm)" package="5 mm [THT]"]
  LED2 = LED - 5mm [color="Yellow (595nm)" package="5 mm [THT]"]
  LED3 = LED - 5mm [color="Green (555nm)" package="5 mm [THT]"]
  R1 = Resistor [tolerance=±5% resistance=220 package=THT]
  R2 = Resistor [tolerance=±5% resistance=220 package=THT]
  R3 = Resistor [tolerance=±5% resistance=220 package=THT]
  Componente2 = Bluetooth HC-05 Macho  # not connected
  R4 = Resistor [tolerance=±5% resistance=1k package=THT]
  R5 = Resistor [tolerance=±5% resistance=1k package=THT]
  R6 = Resistor [tolerance=±5% resistance=1k package=THT]

nets:
  N1: Componente1.D1/TX, R6.Pin_1
  N2: Componente1.D5_PWM, R3.Pin_1
  N3: Componente1.D6_PWM, R2.Pin_1
  N4: Componente1.D7, R1.Pin_1
  N5: Componente1.GND, LED1.cathode, LED2.cathode, LED3.cathode, R4.Pin_0
  N6: LED1.anode, R1.Pin_0
  N7: LED2.anode, R2.Pin_0
  N8: LED3.anode, R3.Pin_0
  N9: R4.Pin_1, R5.Pin_0
  N10: R5.Pin_1, R6.Pin_0
