# Fritzing sketch id1651_Dtmf_8870 (saved by Fritzing 0.5.2b)
breadboards: 1

parts:
  XTAL1 = Crystal
  J1 = Screw terminal - 2 pins [package=THT]
  C3 = Ceramic Capacitor [capacitance=0.1µF rated_voltage=35V package="100 mil [THT, multilayer]"]
  C2 = Ceramic Capacitor [capacitance=0.1µF rated_voltage=35V package="100 mil [THT, multilayer]"]
  Arduino1 = Arduino
  R2 = Resistor [resistance=100k package=THT]
  R3 = Resistor [resistance=100k package=THT]
  IC1 = IC, DIP package, 18 pins [chip_label="IC 8870" spacing=300mil]
  R4 = Resistor [resistance=330k package=THT]
  R1 = Resistor [resistance=100k package=THT]

nets:
  N1: XTAL1.connector0, IC1.pin7
  N2: XTAL1.connector1, IC1.pin8
  N3: J1.pin1, C3.0
  N4: J1.pin2, R1.Pin_0
  N5: C3.1, R2.Pin_1
  N6: C2.0, Arduino1.3V3, IC1.pin10, IC1.pin18
  N7: C2.1, IC1.pin17, R4.Pin_1
  N8: Arduino1.D6, IC1.pin15
  N9: Arduino1.D5, IC1.pin14
  N10: Arduino1.D4, IC1.pin13
  N11: Arduino1.D3, IC1.pin12
  N12: Arduino1.D2, IC1.pin11
  N13: Arduino1.GND, IC1.pin5, IC1.pin6, IC1.pin9, R1.Pin_1
  N14: R2.Pin_0, R3.Pin_1, IC1.pin2
  N15: R3.Pin_0, IC1.pin3
  N16: IC1.pin1, IC1.pin4
  N17: IC1.pin16, R4.Pin_0
