# Fritzing sketch id1651_ESP8266_ESP01_0 (saved by Fritzing 0.9.2b)
breadboards: 1

parts:
  R1 = Resistor [tolerance=±5% resistance=300 package=THT]
  R2 = Resistor [tolerance=±5% resistance=300 package=THT]
  R3 = Resistor [tolerance=±5% resistance=1k package=THT]
  U2 = ESP8266_module [part_number=ESP8266]
  Componente1 = Arduino Uno (Rev3) - ICSP

nets:
  N1: R1.Pin_0, Componente1.D8
  N2: R1.Pin_1, R2.Pin_0, U2.connector0
  N3: R2.Pin_1, U2.connector6, Componente1.GND
  N4: R3.Pin_0, U2.connector5
  N5: R3.Pin_1, U2.connector1, Componente1.3V3
  N6: U2.connector7, Componente1.D9_PWM
