# Fritzing sketch id1652_cutout3_0 (saved by Fritzing 0.9.3b)
breadboards: 1
stripboards: 2

parts:
  Part1 = Arduino Uno (Rev3)
  DRV_1 = DRV 8825 Stepper Motor Carrier, High Current [part_number="DRV 8825"]  # not connected
  LED1 = LED - 3mm [color="Green (570nm)" package="3 mm [THT]"]
  LED2 = LED - 3mm [color="Green (570nm)" package="3 mm [THT]"]
  LED3 = LED - 3mm [color="Green (570nm)" package="3 mm [THT]"]
  LED4 = LED - 3mm [color="Yellow (595nm)" package="3 mm [THT]"]
  LED5 = LED - 3mm [color="Yellow (595nm)" package="3 mm [THT]"]
  LED6 = LED - 3mm [color="Red (660nm)" package="3 mm [THT]"]
  S1 = Pushbutton [package="[THT]"]
  M1 = Stepper Motor - Bipolar
  VCC1 = Battery block 9V [part_number=+12V]
  R1 = Resistor [tolerance=±5% resistance=220 package=THT]
  R2 = Resistor [tolerance=±5% resistance=220 package=THT]
  R3 = Resistor [tolerance=±5% resistance=220 package=THT]
  R4 = Resistor [tolerance=±5% resistance=220 package=THT]
  R5 = Resistor [tolerance=±5% resistance=220 package=THT]
  R6 = Resistor [tolerance=±5% resistance=220 package=THT]
  R7 = Resistor [tolerance=±5% resistance=10k package=THT]
  C1 = Capacitor Polarized [package=cpol-radial-10uf-25v]
  M2 = Stepper Motor - Bipolar
  JP1 = RCA [package=rca_lock]
  U1 = POT [package=alps_pot]
  U2 = Optocoupler [package=THT]
  R8 = Resistor [tolerance=±5% resistance=330 package=THT]
  D1 = Rectifier Diode 10A [part_number=P1000K]
  D2 = Rectifier Diode 10A [part_number=P1000K]
  D3 = Rectifier Diode 10A [part_number=P1000K]
  R9 = Resistor [tolerance=±5% resistance=330 package=THT]
  R10 = Resistor [tolerance=±5% resistance=10k package=THT]
  F1 = FUSE [package=fuse_5mm]
  DRV_2 = DRV 8825 Stepper Motor Carrier, High Current [part_number="DRV 8825"]  # not connected
  C2 = Capacitor Polarized [package=cpol-radial-10uf-25v]
  U3 = Optocoupler [package=THT]
  R11 = Resistor [tolerance=±5% resistance=10k package=THT]
  D4 = Rectifier Diode 10A [part_number=P1000K]
  R12 = Resistor [tolerance=±5% resistance=330 package=THT]
  D5 = Rectifier Diode 10A [part_number=P1000K]
  D6 = Rectifier Diode 10A [part_number=P1000K]
  R13 = Resistor [tolerance=±5% resistance=330 package=THT]
  R14 = Resistor [tolerance=±5% resistance=10k package=THT]
  LED7 = LED - 3mm [color="Green (570nm)" package="3 mm [THT]"]
  LED8 = LED - 3mm [color="Green (570nm)" package="3 mm [THT]"]
  LED9 = LED - 3mm [color="Green (570nm)" package="3 mm [THT]"]
  LED10 = LED - 3mm [color="Yellow (595nm)" package="3 mm [THT]"]
  LED11 = LED - 3mm [color="Yellow (592nm)" package="3 mm [THT]"]
  LED12 = LED - 3mm [color="Red (635nm)" package="3 mm [THT]"]
  R15 = Resistor [tolerance=±5% resistance=330 package=THT]
  R16 = Resistor [tolerance=±5% resistance=330 package=THT]
  R17 = Resistor [tolerance=±5% resistance=330 package=THT]
  R18 = Resistor [tolerance=±5% resistance=330 package=THT]
  R19 = Resistor [tolerance=±5% resistance=330 package=THT]
  R20 = Resistor [tolerance=±5% resistance=330 package=THT]
  S2 = Toggle Switch [package=THT]
  S3 = Pushbutton [package="[THT]"]

nets:
  N1: Part1.A0, U1.S
  N2: Part1.D8, LED2.anode
  N3: Part1.D9_PWM, LED3.anode
  N4: Part1.D10_PWM/SS, LED4.anode
  N5: Part1.D11_PWM/MOSI, LED5.anode
  N6: Part1.D12/MISO, LED6.anode
  N7: Part1.D2, U2.Pin_5, R10.Pin_0
  N8: Part1.D6_PWM, S1.Pin_3, S1.Pin_4
  N9: Part1.D7, LED1.anode
  N10: Part1.5V, R10.Pin_1
  N11: Part1.GND, VCC1.-, R1.Pin_0, R2.Pin_0, R3.Pin_0, R4.Pin_0, R5.Pin_0, R6.Pin_0, R7.Pin_0, C1.-, U2.Pin_4
  N12: Part1.VIN, C1.+, F1.1
  N13: LED1.cathode, R1.Pin_1
  N14: LED2.cathode, R2.Pin_1
  N15: LED3.cathode, R3.Pin_1
  N16: LED4.cathode, R4.Pin_1
  N17: LED5.cathode, R5.Pin_1
  N18: LED6.cathode, R6.Pin_1
  N19: S1.Pin_1, S1.Pin_2, R7.Pin_1
  N20: M1.A, M2.A
  N21: M1.C, M2.C
  N22: M1.B, M2.B
  N23: M1.D, M2.D
  N24: JP1.PIN, R8.Pin_0
  N25: JP1.SHELL, U2.Pin_2, R9.Pin_0
  N26: U2.Pin_1, D2.cathode, D3.cathode
  N27: R8.Pin_1, D1.anode
  N28: D1.cathode, D2.anode
  N29: D3.anode, R9.Pin_1
  N30: C2.+, C2.-, U3.Pin_1, U3.Pin_2, U3.Pin_3, U3.Pin_4, U3.Pin_5, U3.Pin_6, R11.Pin_0, R11.Pin_1, D4.cathode, R12.Pin_0, D5.cathode, D5.anode, D6.cathode, D6.anode, R13.Pin_1
  N31: D4.anode, R12.Pin_1
  N32: R14.Pin_0, R15.Pin_0, R16.Pin_0, R17.Pin_0, R18.Pin_0, R19.Pin_0, R20.Pin_0
  N33: R14.Pin_1, LED7.cathode, LED8.cathode, LED9.cathode, LED10.cathode, LED11.cathode, LED12.cathode, R15.Pin_1, R16.Pin_1, R17.Pin_1, R18.Pin_1, R19.Pin_1, R20.Pin_1, S2.COM, S2.L2, S3.Pin_1, S3.Pin_2
  N34: LED7.anode, LED8.anode, LED9.anode, LED10.anode, LED11.anode, LED12.anode, S2.L1, S3.Pin_3, S3.Pin_4

notes:
  GasPedal connector (Pin4)
  Coil spark input signal (brown/gray)
  +12V
  1A...3A
  NEMA 17 max 350mA
  One cylinder
  Car
  Car aux power
  +5V
  GND
  Spark
  +12v
  D3,D4,D5
  D2
  Motor
  D6
  D7-D12
  power switch +12v
