# Fritzing sketch id1653_Ultra_LCS_Aj_0 (saved by Fritzing 0.9.2b)
breadboards: 1

parts:
  U1 = Hc-SR04-AJ [chip_label=?]
  Part1 = Arduino Uno (Rev3)
  RG1602A = LCD-16X2 [package=lcd-16x2_noholes]
  R4 = Resistor [tolerance=±5% resistance=1.5k package=THT]
  D2 = Rectifier Diode [part_number=1N4148 package="300 mil [THT]"]
  C1 = Ceramic Capacitor [capacitance=100nF package="100 mil [THT, multilayer]"]
  R3 = TRIMPOT [part_number=10K package=trimpot_tc33]
  R1 = Resistor [tolerance=±5% resistance=220k package=THT]
  R2 = Resistor [tolerance=±5% resistance=6.8k package=THT]
  D1 = Rectifier Diode [part_number=1N4148 package="300 mil [THT]"]
  U1_CD40106 = CD40106

nets:
  5V: U1.connector0, Part1.5V, RG1602A.VDD, R4.Pin_1, R3.CCW, R1.Pin_0, U1_CD40106.connector13
  N1: U1.connector1, Part1.D10_PWM/SS, U1_CD40106.connector0
  N2: U1.connector2, Part1.D9_PWM
  GND: U1.connector3, Part1.GND, RG1602A.VSS, RG1602A.R_W, RG1602A.K, C1.0, R3.CW, U1_CD40106.connector6
  N3: U1.connector4, D2.anode
  N4: Part1.D11_PWM/MOSI, RG1602A.E
  N5: Part1.D12/MISO, RG1602A.RS
  N6: Part1.D2, RG1602A.DB7
  N7: Part1.D3_PWM, RG1602A.DB6
  N8: Part1.D4, RG1602A.DB5
  N9: Part1.D5_PWM, RG1602A.DB4
  N10: RG1602A.VO, R3.WIPER
  N11: RG1602A.A, R4.Pin_0
  N12: D2.cathode, R2.Pin_1
  N13: C1.1, R1.Pin_1, D1.anode, U1_CD40106.connector2
  N14: R2.Pin_0, U1_CD40106.connector5
  N15: D1.cathode, U1_CD40106.connector1
  N16: U1_CD40106.connector3, U1_CD40106.connector4
