# Fritzing sketch id1654_Circuit_r2 (saved by Fritzing 0.6.3b)
breadboards: 1

parts:
  IC1 = IC, DIP package, 18 pins [chip_label=IC spacing=300mil]
  J1 = Screw terminal - 2 pins [package=THT]
  IC2 = IC, DIP package, 18 pins [chip_label=IC spacing=300mil]
  J5 = female pin header, 6 pins [form="♀ (female)"]
  J8 = female pin header, 5 pins [form="♀ (female)"]
  J7 = female pin header, 5 pins [form="♀ (female)"]
  J6 = female pin header, 6 pins [form="♀ (female)"]
  J9 = female pin header, 4 pins [form="♀ (female)"]
  Arduino2 = Arduino

nets:
  N1: IC1.pin1, IC1.pin2, Arduino2.D2
  N2: IC1.pin3, IC1.pin4, Arduino2.D3
  N3: IC1.pin5, IC1.pin6, Arduino2.D4
  N4: IC1.pin7, IC1.pin8, Arduino2.D5
  N5: IC1.pin9, J1.pin2, IC2.pin9, J6.pin2, J6.pin3, Arduino2.GND
  N6: IC1.pin10, J1.pin1, IC2.pin10, J8.pin5, J7.pin5
  N7: IC1.pin11, IC1.pin12, J8.pin4
  N8: IC1.pin13, IC1.pin14, J8.pin3
  N9: IC1.pin15, IC1.pin16, J8.pin2
  N10: IC1.pin17, IC1.pin18, J8.pin1
  N11: IC2.pin1, IC2.pin2, Arduino2.D6
  N12: IC2.pin3, IC2.pin4, Arduino2.D7
  N13: IC2.pin5, IC2.pin6, Arduino2.D8
  N14: IC2.pin7, IC2.pin8, Arduino2.D9
  N15: IC2.pin11, IC2.pin12, J7.pin4
  N16: IC2.pin13, IC2.pin14, J7.pin3
  N17: IC2.pin15, IC2.pin16, J7.pin2
  N18: IC2.pin17, IC2.pin18, J7.pin1
  N19: J5.pin1, Arduino2.A5
  N20: J5.pin2, Arduino2.A4
  N21: J5.pin3, Arduino2.A3
  N22: J5.pin4, Arduino2.A2
  N23: J5.pin5, Arduino2.A1
  N24: J5.pin6, Arduino2.A0
  N25: J6.pin1, Arduino2.VIN
  N26: J6.pin4, Arduino2.+5V
  N27: J6.pin5, Arduino2.3V3
  N28: J6.pin6, Arduino2.RST
  N29: J9.pin1, Arduino2.D10
  N30: J9.pin2, Arduino2.D11
  N31: J9.pin3, Arduino2.D12
  N32: J9.pin4, Arduino2.D13

notes:
  Andrew Downey
  Ground
  12V
