# Fritzing sketch id1654_Ventilator_versie_2_0 (saved by Fritzing 0.9.1b)
circuit board: 8.46667cm x 5.64444cm
breadboards: 1

parts:
  Arduino = Arduino Uno (Rev3)
  Motor_controller = L293D [package=THT]
  12_Ingang = Screw terminal - 2 pins [package=THT]
  Motor_uit = Screw terminal - 2 pins [package=THT]
  Temp_Sensor = screw terminal, 3 pins
  R1 = Resistor [tolerance=±5% resistance=4.7k package=THT]
  R2 = Trimmer Potentiometer [maximum_resistance=10kΩ package=THT]
  LDR = Screw terminal - 2 pins [package=THT]
  R3 = Resistor [tolerance=±5% resistance=10k package=THT]

nets:
  N1: Arduino.A0, LDR.pin1, R3.Pin_1
  N2: Arduino.A1, R2.wiper
  N3: Arduino.D9_PWM, Motor_controller.Enable_1
  N4: Arduino.GND, Motor_controller.0V, 12_Ingang.pin2, Temp_Sensor.pin2, R2.leg1, R3.Pin_0
  N5: Arduino.D2, Temp_Sensor.pin3, R1.Pin_0
  N6: Arduino.D3_PWM, Motor_controller.In_2
  N7: Arduino.D4, Motor_controller.In_1
  N8: Arduino.5V, Motor_controller.+V, Temp_Sensor.pin1, R1.Pin_1, R2.leg2, LDR.pin2
  N9: Motor_controller.Out_1_(_Controlled_by_Enable_1_), Motor_uit.pin2
  N10: Motor_controller.Out_2_(_Controlled_by_Enable_1_), Motor_uit.pin1
  N11: Motor_controller.+Vmotor, 12_Ingang.pin1
