# Fritzing sketch id1656_post5_1_0 (saved by Fritzing 0.8.7b)
breadboards: 1

parts:
  Part1 = Arduino Uno (Rev3)
  S1 = SWITCH-MOMENTARY-2 [package=tactile_switch_smd-2]

nets:
  N1: Part1.D5_PWM, S1.1
