# Fritzing sketch id1658_RBG_LED_Sketch_0 (saved by Fritzing 0.9.1b)
breadboards: 1

parts:
  Part1 = Arduino Uno (Rev3)
  S1 = Pushbutton [package="[SMD]"]
  S2 = Pushbutton [package="[SMD]"]
  LED1 = RGB LED (com. cathode, rgb) [package="5 mm [THT]"]
  R1 = Resistor [tolerance=±5% resistance=1k package=THT]
  R2 = Resistor [tolerance=±5% resistance=1k package=THT]

nets:
  N1: Part1.D8, S1.Pin_3, S1.Pin_4, R1.Pin_1
  N2: Part1.D9_PWM, S2.Pin_3, S2.Pin_4, R2.Pin_1
  N3: Part1.D3_PWM, LED1.blue_anode
  N4: Part1.D5_PWM, LED1.common_cathode
  N5: Part1.D6_PWM, LED1.red_anode
  N6: S1.Pin_1, S1.Pin_2, LED1.green_anode
  N7: S2.Pin_1, S2.Pin_2, R1.Pin_0, R2.Pin_0
