# Fritzing sketch id1659_relogiobomba_0 (saved by Fritzing 0.9.2b)
circuit board: 10.1224cm x 5.60143cm

parts:
  Componente1 = Arduino Nano (Rev3.0)
  Componente2 = Real Time Clock Module - DS1307 RTC Breakout Board
  LED_Verde = LED - 3mm [color="Green (560nm)" package="3 mm [THT]"]
  LED_VERMELHO = LED - 3mm [color="Red (633nm)" package="3 mm [THT]"]
  R1 = Resistor [tolerance=±5% resistance=470 package="0603 [SMD]"]
  R2 = Resistor [tolerance=±5% resistance=470 package="0603 [SMD]"]
  CHAVE = Toggle Switch [package=THT]
  POWER_5V = Power plug
  DISPLAY = Grove 4 Digit Display
  J1 = Piezo Speaker

nets:
  GND: Componente1.GND, Componente2.GND, LED_Verde.cathode, LED_VERMELHO.cathode, CHAVE.COM, POWER_5V.GND, DISPLAY.GND, J1.pin1
  N1: Componente1.D6, J1.pin2
  N2: Componente1.D7, CHAVE.L2
  N3: Componente1.D8, DISPLAY.DIO
  N4: Componente1.D9, DISPLAY.CLK
  N5: Componente1.D10, R1.Pin_1
  N6: Componente1.D11/MOSI, R2.Pin_1
  VIN: Componente1.VIN, POWER_5V.VCC
  5V: Componente1.5V, Componente2.5V, DISPLAY.VCC
  N7: Componente1.A5, Componente2.SCL
  N8: Componente1.A4, Componente2.SDA
  N9: LED_Verde.anode, R2.Pin_0
  N10: LED_VERMELHO.anode, R1.Pin_0

notes:
  Entrada 5v
