# Fritzing sketch id165_6+ardu+ether_0 (saved by Fritzing 0.8.5b)
circuit board: 11.1102cm x 5.63504cm
breadboards: 1

parts:
  Parte1 = Arduino Pro Mini v13
  U1 = Optocoupler [package=THT]
  U2 = Optocoupler [package=THT]
  U3 = Optocoupler [package=THT]
  U4 = Optocoupler [package=THT]
  U5 = Optocoupler [package=THT]
  U6 = Optocoupler [package=THT]
  LED1 = LED - 5mm [color="Red (633nm)" package="5 mm [THT]"]
  LED2 = LED - 5mm [color="Red (633nm)" package="5 mm [THT]"]
  LED3 = LED - 5mm [color="Red (633nm)" package="5 mm [THT]"]
  LED4 = LED - 5mm [color="Red (633nm)" package="5 mm [THT]"]
  LED5 = LED - 5mm [color="Red (633nm)" package="5 mm [THT]"]
  LED6 = LED - 5mm [color="Red (633nm)" package="5 mm [THT]"]
  R1 = Resistor [tolerance=±5% resistance=220 package=THT]
  R2 = Resistor [tolerance=±5% resistance=220 package=THT]
  R3 = Resistor [tolerance=±5% resistance=220 package=THT]
  R4 = Resistor [tolerance=±5% resistance=220 package=THT]
  R5 = Resistor [tolerance=±5% resistance=220 package=THT]
  R6 = Resistor [tolerance=±5% resistance=220 package=THT]
  J1 = female pin header, 2 pins [form="♀ (female)"]
  J2 = female pin header, 2 pins [form="♀ (female)"]
  J3 = female pin header, 2 pins [form="♀ (female)"]
  J4 = female pin header, 2 pins [form="♀ (female)"]
  J5 = female pin header, 2 pins [form="♀ (female)"]
  J6 = female pin header, 2 pins [form="♀ (female)"]
  R7 = Resistor [tolerance=±5% resistance=220 package=THT]
  R8 = Resistor [tolerance=±5% resistance=220 package=THT]
  R9 = Resistor [tolerance=±5% resistance=220 package=THT]
  R10 = Resistor [tolerance=±5% resistance=220 package=THT]
  R11 = Resistor [tolerance=±5% resistance=220 package=THT]
  R12 = Resistor [tolerance=±5% resistance=220 package=THT]
  U7 = WIZ811MJ [package=wiz811mj]
  J7 = female alternating pin header, 6 pins [form="♀ (female)"]

nets (from the pcb view):
  N1: Parte1.DTR, U7.GND, J7.pin6
  N2: Parte1.D0/TX, J7.pin5
  N3: Parte1.D1/RX, J7.pin4
  VCC: Parte1.VCC, R7.Pin_0, R8.Pin_0, R9.Pin_0, R10.Pin_0, R11.Pin_0, R12.Pin_0, U7.VCC, J7.pin3
  N4: Parte1.GND, U1.Pin_4, U2.Pin_4, U3.Pin_4, U4.Pin_4, U5.Pin_4, U6.Pin_4, J7.pin1, J7.pin2
  N5: Parte1.D13/SCK, U7.SCLK
  N6: Parte1.D12/MISO, U7.MISO
  N7: Parte1.D11_PWM/MOSI, U7.MOSI
  N8: Parte1.D10_PWM/SS, U7._SCS
  N9: Parte1.D8, U6.Pin_6, R12.Pin_1
  N10: Parte1.D7, U5.Pin_6, R11.Pin_1
  N11: Parte1.D6_PWM, U4.Pin_6, R10.Pin_1
  N12: Parte1.D5_PWM, U3.Pin_6, R9.Pin_1
  N13: Parte1.D4, U2.Pin_6, R8.Pin_1
  N14: Parte1.D3_PWM, U1.Pin_6, R7.Pin_1
  N15: U1.Pin_1, LED1.anode, R6.Pin_0
  N16: U1.Pin_2, LED1.cathode, J1.pin1
  N17: U2.Pin_1, LED2.anode, R5.Pin_0
  N18: U2.Pin_2, LED2.cathode, J2.pin1
  N19: U3.Pin_1, LED3.anode, R4.Pin_0
  N20: U3.Pin_2, LED3.cathode, J3.pin1
  N21: U4.Pin_1, LED4.anode, R3.Pin_1
  N22: U4.Pin_2, LED4.cathode, J4.pin1
  N23: U5.Pin_1, LED5.anode, R2.Pin_0
  N24: U5.Pin_2, LED5.cathode, J5.pin1
  N25: U6.Pin_1, LED6.anode, R1.Pin_0
  N26: U6.Pin_2, LED6.cathode, J6.pin1
  N27: R1.Pin_1, J6.pin2
  N28: R2.Pin_1, J5.pin2
  N29: R3.Pin_0, J4.pin2
  N30: R4.Pin_1, J3.pin2
  N31: R5.Pin_1, J2.pin2
  N32: R6.Pin_1, J1.pin2
