# Fritzing sketch id1660_fame_demo_0 (saved by Fritzing 0.9.2b)
breadboards: 1

parts:
  R1 = Resistor [tolerance=±5% resistance=220 package=THT]
  LED1 = LED - 5mm [color="Red (633nm)" package="5 mm [THT]"]
  Part1 = Arduino Uno (Rev3)
  J1 = female pin header, 2 pins [form="♀ (female)"]

nets:
  N1: R1.Pin_0, Part1.5V
  N2: R1.Pin_1, LED1.anode, Part1.D12/MISO, J1.pin2
  N3: LED1.cathode, Part1.GND
