# Fritzing sketch id1661_duin (saved by Fritzing 0.4.2b)

parts:
  Q1 = PNP-Transistor [package="TO92 [THT]"]
  Power_plug1 = Power plug
  R1 = Resistor [resistance=10k package=THT]
  LED1 = white LED - 5mm  # not connected
  Arduino1 = Arduino Mega
  U1 = Optocoupler [package=THT]  # not connected
  U2 = Voltage Regulator - 5V [package="TO220 [THT]"]  # not connected
  USB1 = Wiring USB Adapter  # not connected
  DC_Power1 = DC Power [voltage=5]  # not connected

nets:
  N1: Q1.E, Power_plug1.VCC
  N2: Q1.B, Arduino1.A2
  N3: Q1.C, R1.Pin_0

notes:
  nofxx
