# Fritzing sketch id1661_nano_dht22_fans_0 (saved by Fritzing 0.9.2b)
breadboards: 1

parts:
  Composant1 = Arduino Nano (Rev3.0)
  RHT1 = Humidity and Temperature Sensor RHT03
  M1 = DC Motor
  M2 = DC Motor

nets:
  N1: Composant1.GND, RHT1.GND_2, M1.pin_2, M2.pin_2
  N2: Composant1.D4, M1.pin_1
  N3: Composant1.D7, M2.pin_1
  N4: Composant1.D9, RHT1.GND_1
  5V: Composant1.5V, RHT1.Vcc
