# Fritzing sketch id1662_fan_temp_0 (saved by Fritzing 0.9.3b)
breadboards: 2

parts:
  BD139 = npn-Powertransistor [package="TO220 [THT]"]
  Pot = Rotary Potentiometer (Small) [maximum_resistance=10kΩ package=THT]
  LCD_16x2 = LCD screen
  Diode = Rectifier Diode [part_number=1N4007 package="300 mil [THT]"]
  Temp_Sensor = LM35 Temperature Sensor [package="TO92 [THT]"]
  R2 = Resistor [tolerance=±5% resistance=1k package=THT]
  Part1 = Arduino Nano (Rev3.0)
  LED2 = LED - 5mm [color="Red (633nm)" package="5 mm [THT]"]
  R3 = Resistor [tolerance=±5% resistance=1k package=THT]
  VCC1 = 4 x AAA Battery Mount
  M2 = DC Motor
  C1 = Electrolytic Capacitor [capacitance=100μF voltage=50V package="0807 [SMD, electrolytic]"]

nets:
  GND: BD139.base, Pot.leg1, LCD_16x2.VSS, LCD_16x2.R/W, LCD_16x2.LED-, Temp_Sensor.GND, Part1.GND, LED2.cathode, VCC1.-, C1.-
  N1: BD139.collector, Diode.anode, M2.pin_2
  N2: BD139.emitter, R2.Pin_1, C1.+
  N3: Pot.wiper, LCD_16x2.V0
  VDD: Pot.leg2, LCD_16x2.VDD, LCD_16x2.LED+, Temp_Sensor.+Vs, Part1.5V
  N4: LCD_16x2.RS, Part1.D7
  N5: LCD_16x2.E, Part1.D6
  N6: LCD_16x2.DB4, Part1.D5
  N7: LCD_16x2.DB5, Part1.D4
  N8: LCD_16x2.DB6, Part1.D3
  N9: LCD_16x2.DB7, Part1.D2
  N10: Diode.cathode, VCC1.+, M2.pin_1
  N11: Temp_Sensor.Vout, Part1.A1
  N12: R2.Pin_0, Part1.D11/MOSI
  N13: Part1.D8, R3.Pin_0
  N14: LED2.anode, R3.Pin_1

notes:
  4xAA Batteries
  6V for Fan
  R = 1kOhm
  Diode: 1N4007
  Transistor: BD139
  Capacitor: 100uF/50V
  Fan (DC Motor)
  LCD 16x2
  10kOhm Pot
  Arduino Nano R3
  LED ON at Max Temp.
  R = 1kOhm
  Sensor: LM35
  I powered the Nano through the USB Cable from my PC
