# Fritzing sketch id1663_FAN__0 (saved by Fritzing 0.9.2b)
breadboards: 1

parts:
  Part1 = Arduino Uno (Rev3)
  T1 = LM35 Temperature Sensor [package="TO92 [THT]"]
  U1 = LCD-16X2 [package=lcd-16x2_noholes]  # not connected
  R1 = Resistor [tolerance=±5% resistance=220 package=THT]
  U2 = DIODE-ZENER [package=diode-zener]
  R2 = Resistor [tolerance=±5% resistance=220 package=THT]

nets:
  N1: Part1.D7, R2.Pin_0
  GND: Part1.GND, T1.GND, R1.Pin_1, U2.C

notes:
  on frizing don't has fan the fan has two black wire on pin 7 and red wire on ground (gnd)
