# Fritzing sketch id1665_fatto_in_casa_0 (saved by Fritzing 0.8.7b)
circuit board: 7.2107cm x 6.14113cm
breadboards: 1

parts:
  J1 = female pin header, 6 pins [form="♀ (female)"]
  J2 = female pin header, 6 pins [form="♀ (female)"]
  J3 = female pin header, 8 pins [form="♀ (female)"]
  J4 = female pin header, 8 pins [form="♀ (female)"]
  J6 = male pin header, 6 pins [form="♂ (male)"]
  Power_plug1 = Power plug
  jumper = Toggle Switch [package=THT]
  1N4007 = Rectifier Diode [part_number=1N4007 package="300 mil [THT]"]
  22pF = Ceramic Capacitor [capacitance=100nF package="100 mil [THT, multilayer]"]
  22pF_2 = Ceramic Capacitor [capacitance=10pF package="100 mil [THT, multilayer]"]
  0_1uF = Ceramic Capacitor [capacitance=100nF package="200 mil [THT, multilayer]"]
  LED = LED - 3mm [color="Red (633nm)" package="3 mm [THT]"]
  1K = Resistor [tolerance=±5% resistance=1k package=THT]
  LED_2 = LED - 3mm [color="Red (633nm)" package="3 mm [THT]"]
  RST = Pushbutton [package="[THT]"]
  10K = Resistor [tolerance=±5% resistance=10k package=THT]
  1K_2 = Resistor [tolerance=±5% resistance=1k package=THT]
  7805 = Voltage Regulator - 5V [package="TO220 [THT]"]
  100uF = Electrolytic Capacitor [capacitance=47µF voltage=20V package="100 mil [THT, electrolytic]"]
  100uF_2 = Electrolytic Capacitor [capacitance=47µF voltage=20V package="100 mil [THT, electrolytic]"]
  10nF = Ceramic Capacitor [capacitance=10nF package="100 mil [THT, multilayer]"]
  ATMEGA328P = atmega328 [part_number="ATMEGA 328" package=dip]
  16Mhz = Crystal [frequency="16 Mhz" package=THT]

nets:
  N1: J1.pin1, ATMEGA328P.A5
  N2: J1.pin2, ATMEGA328P.A4
  N3: J1.pin3, ATMEGA328P.A3
  N4: J1.pin4, ATMEGA328P.A2
  N5: J1.pin5, ATMEGA328P.A1
  N6: J1.pin6, ATMEGA328P.A0
  N7: J2.pin1, 1N4007.cathode, 7805.input_voltage, 100uF_2.+
  GND: J2.pin2, J2.pin3, J4.pin7, J6.pin6, Power_plug1.GND, 22pF.0, 22pF_2.1, 1K.Pin_0, RST.Pin_4, 1K_2.Pin_1, 7805.GND, 100uF.-, 100uF_2.-, 10nF.1, ATMEGA328P.GND
  N8: J2.pin4, jumper.COM, LED_2.anode, 10K.Pin_1, ATMEGA328P.VCC, ATMEGA328P.AVCC
  N9: J2.pin6, J6.pin1, 0_1uF.1
  N10: J3.pin1, J6.pin3, ATMEGA328P.D0_(RX)
  N11: J3.pin2, J6.pin2, ATMEGA328P.D1_(TX)
  N12: J3.pin3, ATMEGA328P.D2
  N13: J3.pin4, ATMEGA328P.D3_(PWM)
  N14: J3.pin5, ATMEGA328P.D4
  N15: J3.pin6, ATMEGA328P.D5_(PWM)
  N16: J3.pin7, ATMEGA328P.D6_(PWM)
  N17: J3.pin8, ATMEGA328P.D7
  N18: J4.pin1, ATMEGA328P.D8
  N19: J4.pin2, ATMEGA328P.D9_(PWM)
  N20: J4.pin3, ATMEGA328P.D10_(PWM)
  N21: J4.pin4, ATMEGA328P.D11_(PWM)
  N22: J4.pin5, ATMEGA328P.D12
  N23: J4.pin6, LED.anode, ATMEGA328P.D13
  N24: J4.pin8, 10nF.0, ATMEGA328P.AREF
  N25: J6.pin4, jumper.L1
  N26: Power_plug1.VCC, 1N4007.anode
  N27: jumper.L2, 7805.output_voltage, 100uF.+
  N28: 22pF.1, ATMEGA328P.XLAT1, 16Mhz.pin_1
  N29: 22pF_2.0, ATMEGA328P.XLAT2, 16Mhz.pin_0
  N30: 0_1uF.0, RST.Pin_1, RST.Pin_2, 10K.Pin_0, ATMEGA328P.RESET
  N31: LED.cathode, 1K.Pin_1
  N32: LED_2.cathode, 1K_2.Pin_0

notes:
  FATTO IN CASA
  laboratoriodejuguete.com
  2
  ~6
  (TX) 1
  4
  ~3
  7
  ~5
  (RX) 0
  12
  ~9
  ~10
  ~11
  8
  13
  GND
  AREF
  PWM~
  DIGITAL
  ANALOG IN
  3
  5
  1
  0
  USB
  EXT
  5V
  RX
  TX
  DTR
  RST
  Vin
  7/12V
  HLQSTCEC
  laboratoriodejuguete.com, FATTO IN CASA , 2
