# Fritzing sketch id1666_exemplo_para_piscar_o_LED(ou_quantos_quiser)_0 (saved by Fritzing 0.7.12b)
breadboards: 1

parts:
  R1 = Resistor [tolerance=±5% resistance=220 package=THT]
  LED1 = LED - 5mm [color="Red (633nm)" package="5 mm [THT]"]
  R2 = Resistor [tolerance=±5% resistance=220 package=THT]
  LED2 = LED - 5mm [color="Red (633nm)" package="5 mm [THT]"]
  Arduino1 = Arduino

nets:
  N1: R1.Pin_0, R2.Pin_1, Arduino1.GND
  N2: R1.Pin_1, LED1.cathode
  N3: LED1.anode, Arduino1.D13
  N4: R2.Pin_0, LED2.cathode, Arduino1.D5

notes:
  /*
  Blink
  Turns on an LED on for one second, then off for one second, repeatedly.
  This example code is in the public domain.
  */
  void setup() {
  // initialize the digital pin as an output.
  // Pin 13 has an LED connected on most Arduino boards:
  pinMode(13, OUTPUT);
  }
  void loop() {
  digitalWrite(13, HIGH); // set the LED on
  delay(1000); // wait for a second
  digitalWrite(13, LOW); // set the LED off
  delay(1); // wait for a second
  }
