# Fritzing sketch id1667_FDL_1p_0 (saved by Fritzing 0.9.2b)
breadboards: 2

parts:
  S1 = Pushbutton [package="[THT]"]
  JP1 = Header 12 [package=1x12_machine-pin-header_lock.004]
  JP2 = Header 12 [package=1x12_machine-pin-header_lock.004]
  JP3 = Header 8 [package=1x08_smd_alt]
  JP4 = Header 8 [package=1x08_smd_alt]
  JP5 = Header 8 [package=1x08_smd_alt]
  JP6 = Header 8 [package=1x08_smd_alt]
  R1 = Resistor [tolerance=±5% resistance=1k package=THT]
  S2 = Pushbutton [package="[THT]"]
  R2 = Rotary Potentiometer (Small) [maximum_resistance=100kΩ package=THT]
  M2 = Stepper Motor - Bipolar
  M1 = Stepper Motor - Bipolar
  S3 = Pushbutton [package="[THT]"]

nets:
  N1: S1.Pin_3, S1.Pin_4, JP1.12, JP2.1, JP2.2, JP2.4, JP2.10, JP3.2, JP3.3, JP3.5, JP3.6, JP6.2, JP6.3, JP6.5, JP6.6, R1.Pin_0, S2.Pin_3, S2.Pin_4, R2.leg2, S3.Pin_3, S3.Pin_4
  N2: JP1.6, JP6.7
  N3: JP1.7, JP3.7
  N4: JP1.8, JP3.1, JP6.1, R1.Pin_1
  N5: JP1.9, JP4.8, JP5.8
  N6: JP1.11, R2.leg1
  N7: JP2.6, R2.wiper
  N8: JP4.1, JP5.1
  N9: JP4.2, JP5.2
  N10: JP4.3, M2.A
  N11: JP4.4, M2.C
  N12: JP4.5, M2.B
  N13: JP4.6, M2.D
  N14: JP5.3, M1.A
  N15: JP5.4, M1.C
  N16: JP5.5, M1.B
  N17: JP5.6, M1.D

notes:
  (2) DRV8825 Drivers
  Chips On Right Side
  Particle Photon
  USB On Right
  12v
  5v From ESC's
  Orange wire enables wifi
  could be converted to switch
  Advance
  Switch
  Plunger
  Switch
  Trigger
  Switch
  Plunger
  Motor
  Revolver
  Motor
  Speed
  Knob
