# Fritzing sketch id1668_feather_atwinc1500u_RevA1_0 (saved by Fritzing 0.9.3b)
breadboards: 1

parts:
  U1 = Optocoupler [package=THT]
  U2 = Optocoupler [package=THT]
  Part1 = adafruit [part_number="Adafruit #3010"]
  R1 = Resistor [tolerance=±5% resistance=100 package=THT]
  R2 = Resistor [tolerance=±5% resistance=100 package=THT]
  R3 = Resistor [tolerance=±5% resistance=4.7k package=THT]
  R4 = Resistor [tolerance=±5% resistance=4.7k package=THT]
  R5 = Resistor [tolerance=±5% resistance=390 package=THT]
  DOTSTAR1 = adafruit [part_number=2240]

nets:
  N1: U1.Pin_1, R4.Pin_1, R5.Pin_0
  N2: U1.Pin_2, U2.Pin_2, Part1.connector40, DOTSTAR1.connector1
  N3: U1.Pin_4, R1.Pin_0
  N4: U1.Pin_5, U2.Pin_5, Part1.connector34, R3.Pin_0, R4.Pin_0, DOTSTAR1.connector3
  N5: U2.Pin_1, R3.Pin_1, DOTSTAR1.connector7
  N6: U2.Pin_4, R2.Pin_0
  N7: Part1.connector26, R1.Pin_1
  N8: Part1.connector27, R2.Pin_1
  N9: R5.Pin_1, DOTSTAR1.connector2
