# Fritzing sketch id166_6_LED_Matrix_0 (saved by Fritzing 0.5.2b)
breadboards: 1

parts:
  LED1 = Red LED - 5mm [package="5 mm [THT]"]
  LED2 = Red LED - 5mm [package="5 mm [THT]"]
  LED4 = Red LED - 5mm [package="5 mm [THT]"]
  LED5 = Red LED - 5mm [package="5 mm [THT]"]
  LED3 = Red LED - 5mm [package="5 mm [THT]"]
  LED6 = Red LED - 5mm [package="5 mm [THT]"]
  R1 = Resistor [resistance=680 package=THT]
  R2 = Resistor [resistance=680 package=THT]
  R3 = Resistor [resistance=680 package=THT]
  R4 = Resistor [resistance=680 package=THT]
  R5 = Resistor [resistance=680 package=THT]
  R6 = Resistor [resistance=680 package=THT]
  Arduino1 = Arduino

nets:
  N1: LED1.cathode, LED2.cathode, LED4.cathode, LED5.cathode, LED3.cathode, LED6.cathode, Arduino1.GND
  N2: LED1.anode, R1.Pin_0
  N3: LED2.anode, R2.Pin_0
  N4: LED4.anode, R4.Pin_0
  N5: LED5.anode, R5.Pin_0
  N6: LED3.anode, R3.Pin_0
  N7: LED6.anode, R6.Pin_0
  N8: R1.Pin_1, Arduino1.D6
  N9: R2.Pin_1, Arduino1.D5
  N10: R3.Pin_1, Arduino1.D4
  N11: R4.Pin_1, Arduino1.D3
  N12: R5.Pin_1, Arduino1.D2
  N13: R6.Pin_1, Arduino1.D1TX
