# Fritzing sketch id1671_Untitled_Sketch_0 (saved by Fritzing 0.8.7b)
breadboards: 1

parts:
  VCC1 = Battery
  R1 = Resistor [tolerance=±5% resistance=220 package=THT]
  LED1 = LED - 5mm [color="Red (633nm)" package="5 mm [THT]"]

nets:
  N1: VCC1.-, R1.Pin_1
  N2: VCC1.+, LED1.cathode
