# Fritzing sketch id1672_ferro1_0 (saved by Fritzing 0.7.12b)
breadboards: 1

parts:
  Arduino1 = Arduino
  R2 = Rotary Potentiometer (Small) [maximum_resistance=100kΩ]
  R3 = Resistor [tolerance=±5% resistance=220 package=THT]
  D1 = Rectifier Diode [part_number=1N4004 package="300 mil [THT]"]
  Q1 = Basic FET P-Channel [package="TO220 [THT]"]
  LED1 = LED - 5mm [color="Green (560nm)" package="5 mm [THT]"]
  R4 = Resistor [tolerance=±5% resistance=220 package=THT]
  R2_2 = Resistor [tolerance=±5% resistance=220 package=THT]
  R1 = Resistor [tolerance=±5% resistance=10k package=THT]
  Electromagnet = Inductor [package="0805 [SMD]"]
  Power = Power plug [part_number=12v]
  R0 = Resistor [tolerance=±5% resistance=5 package=THT]
  U1 = Optocoupler [package=THT]

nets:
  GND: Arduino1.GND, R2.leg2, Q1.source, R2_2.Pin_1, Power.GND, U1.Pin_2
  N1: Arduino1.D9, LED1.anode
  N2: Arduino1.+5V, R2.leg1, U1.Pin_5
  VIN: Arduino1.VIN, D1.cathode, Electromagnet.pin_1, Power.VCC
  N3: Arduino1.A0, R2.wiper
  N4: R3.Pin_0, U1.Pin_1
  N5: R3.Pin_1, R4.Pin_0
  N6: D1.anode, Q1.drain, R0.Pin_0
  N7: Q1.gate, R2_2.Pin_0, R1.Pin_1
  N8: LED1.cathode, R4.Pin_1
  N9: R1.Pin_0, U1.Pin_4
  N10: Electromagnet.pin_0, R0.Pin_1

notes:
  External 12v DC
  power supply
