# Fritzing sketch id1672_project (saved by Fritzing 0.6.4b)
breadboards: 1

parts:
  Arduino2 = Arduino
  LED1 = LED - 5mm [color="Red (633nm)" package="5 mm [THT]"]
  LED2 = LED - 5mm [color="Red (633nm)" package="5 mm [THT]"]
  LED3 = LED - 5mm [color="Red (633nm)" package="5 mm [THT]"]
  LED4 = LED - 5mm [color="Red (633nm)" package="5 mm [THT]"]
  LED5 = LED - 5mm [color="Red (633nm)" package="5 mm [THT]"]
  LED6 = LED - 5mm [color="Red (633nm)" package="5 mm [THT]"]
  LED7 = LED - 5mm [color="Red (633nm)" package="5 mm [THT]"]

nets:
  N1: Arduino2.GND, LED1.cathode, LED2.cathode, LED3.cathode
  N2: Arduino2.D8, LED1.anode
  N3: Arduino2.D7, LED2.anode
  N4: Arduino2.D6, LED3.anode
  N5: Arduino2.D5, LED4.anode
  N6: Arduino2.D4, LED5.anode
  N7: Arduino2.D3, LED6.anode
  N8: Arduino2.D2, LED7.anode
  N9: LED4.cathode, LED5.cathode, LED6.cathode, LED7.cathode

notes:
  Visit my website
  www.ilnlogdidami.blogspot.com
