# Fritzing sketch id1673_feux_fritzing_0 (saved by Fritzing 0.9.1b)
circuit board: 6.88566cm x 5.36311cm
breadboards: 2

parts:
  LED1 = LED - 5mm [color="Red (633nm)" package="5 mm [THT]"]
  LED2 = LED - 5mm [color="Yellow (592nm)" package="5 mm [THT]"]
  LED3 = LED - 5mm [color="Green (555nm)" package="5 mm [THT]"]
  LED4 = LED - 5mm [color="Red (633nm)" package="5 mm [THT]"]
  LED5 = LED - 5mm [color="Green (555nm)" package="5 mm [THT]"]
  R1 = Resistor [tolerance=±5% resistance=220 package=THT]
  R2 = Resistor [tolerance=±5% resistance=220 package=THT]
  R3 = Resistor [tolerance=±5% resistance=220 package=THT]
  R4 = Resistor [tolerance=±5% resistance=220 package=THT]
  R5 = Resistor [tolerance=±5% resistance=220 package=THT]
  Bouton_poussoir = Pushbutton [package=THT]
  R6 = Resistor [tolerance=±5% resistance=100k package=THT]
  Arduino1 = Arduino Uno (Rev3)

nets:
  N1: LED1.cathode, R1.Pin_0
  N2: LED1.anode, Arduino1.D12/MISO
  N3: LED2.cathode, R2.Pin_0
  N4: LED2.anode, Arduino1.D11_PWM/MOSI
  N5: LED3.cathode, R3.Pin_0
  N6: LED3.anode, Arduino1.D10_PWM/SS
  N7: LED4.cathode, R4.Pin_0
  N8: LED4.anode, Arduino1.D9_PWM
  N9: LED5.cathode, R5.Pin_0
  N10: LED5.anode, Arduino1.D8
  N11: R1.Pin_1, R2.Pin_1, R3.Pin_1, R4.Pin_1, R5.Pin_1, R6.Pin_1, Arduino1.GND
  N12: Bouton_poussoir.leg0, R6.Pin_0, Arduino1.D2
  N13: Bouton_poussoir.leg1, Arduino1.5V

notes:
  Feux Piétons
  Feux
