# Fritzing sketch id1675_FiBiNo_0 (saved by Fritzing 0.9.0b)
breadboards: 2

parts:
  Componente2 = Real Time Clock Module - DS1307 RTC Breakout Board
  S1 = Pushbutton [package="[THT]"]
  S2 = Pushbutton [package="[THT]"]
  S3 = Pushbutton [package="[THT]"]
  LCD1 = LCD screen
  R1 = Resistor [tolerance=±5% resistance=10k package=THT]
  R2 = Resistor [tolerance=±5% resistance=10k package=THT]
  R3 = Resistor [tolerance=±5% resistance=10k package=THT]
  C1 = Ceramic Capacitor [capacitance=100nF package="100 mil [THT, multilayer]"]
  C2 = Electrolytic Capacitor [capacitance=1µF package="100 mil [THT, electrolytic]"]
  Componente4 = Arduino Mega 2560 (Rev3)
  Power_plug1 = Power plug
  U2 = Voltage Regulator - 5V [package="TO220 [THT]"]
  R4 = Resistor [tolerance=±5% resistance=470 package=THT]
  LED1 = LED - 5mm [color="Yellow (585nm)" package="5 mm [THT]"]
  R5 = Resistor [tolerance=±5% resistance=220 package=THT]
  R6 = prefix0000
  R7 = Resistor [tolerance=±5% resistance=470 package=THT]
  R8 = Resistor [tolerance=±5% resistance=470 package=THT]
  R9 = Resistor [tolerance=±5% resistance=470 package=THT]
  R10 = Resistor [tolerance=±5% resistance=470 package=THT]
  R11 = Resistor [tolerance=±5% resistance=470 package=THT]
  R12 = Resistor [tolerance=±5% resistance=470 package=THT]
  R13 = Resistor [tolerance=±5% resistance=470 package=THT]
  R14 = Resistor [tolerance=±5% resistance=470 package=THT]
  R15 = Resistor [tolerance=±5% resistance=470 package=THT]
  R16 = Resistor [tolerance=±5% resistance=470 package=THT]
  R17 = Resistor [tolerance=±5% resistance=470 package=THT]
  LED2 = LED - 5mm [color="Yellow (585nm)" package="5 mm [THT]"]
  LED3 = LED - 5mm [color="Yellow (585nm)" package="5 mm [THT]"]
  LED4 = LED - 5mm [color="Yellow (585nm)" package="5 mm [THT]"]
  LED5 = LED - 5mm [color="Yellow (585nm)" package="5 mm [THT]"]
  LED6 = LED - 5mm [color="Yellow (585nm)" package="5 mm [THT]"]
  LED7 = LED - 5mm [color="Yellow (585nm)" package="5 mm [THT]"]
  LED8 = LED - 5mm [color="Yellow (585nm)" package="5 mm [THT]"]
  LED9 = LED - 5mm [color="Yellow (585nm)" package="5 mm [THT]"]
  LED10 = LED - 5mm [color="Yellow (585nm)" package="5 mm [THT]"]
  LED11 = LED - 5mm [color="Yellow (585nm)" package="5 mm [THT]"]
  LED12 = LED - 5mm [color="Yellow (585nm)" package="5 mm [THT]"]
  Q1 = NPN-Transistor [package="TO92 [THT]"]
  Q2 = NPN-Transistor [package="TO92 [THT]"]
  Q3 = NPN-Transistor [package="TO92 [THT]"]
  R19 = Resistor [tolerance=±5% resistance=470 package=THT]
  R20 = Resistor [tolerance=±5% resistance=470 package=THT]
  R21 = Resistor [tolerance=±5% resistance=470 package=THT]
  R22 = Resistor [tolerance=±5% resistance=470 package=THT]
  LED13 = LED - 5mm [color="White (8000K)" package="5 mm [THT]"]
  LED14 = LED - 5mm [color="Green (555nm)" package="5 mm [THT]"]  # not connected
  LED15 = LED - 5mm [color="Blue (525nm)" package="5 mm [THT]"]  # not connected
  LED16 = LED - 5mm [color="Red (633nm)" package="5 mm [THT]"]
  R23 = Resistor [tolerance=±5% resistance=10k package=THT]
  R24 = Resistor [tolerance=±5% resistance=10k package=THT]
  R25 = Resistor [tolerance=±5% resistance=10k package=THT]
  R26 = Resistor [tolerance=±5% resistance=470 package=THT]
  LED18 = LED - 5mm [color="White (8000K)" package="5 mm [THT]"]
  LED19 = LED - 5mm [color="Red (633nm)" package="5 mm [THT]"]  # not connected
  LED20 = LED - 5mm [color="Red (633nm)" package="5 mm [THT]"]  # not connected
  LED21 = LED - 5mm [color="Red (633nm)" package="5 mm [THT]"]  # not connected
  LED22 = LED - 5mm [color="Red (633nm)" package="5 mm [THT]"]
  LED23 = LED - 5mm [color="Blue (525nm)" package="5 mm [THT]"]
  LED24 = LED - 5mm [color="Blue (525nm)" package="5 mm [THT]"]
  LED25 = LED - 5mm [color="Green (555nm)" package="5 mm [THT]"]
  LCM1602_IIC1 = generic_ic_dip_22_300mil.fzp [part_number="LCM1602 IIC" chip_label="LCM1602 IIC"]
  D2 = Rectifier Diode [part_number=1N4001 package="300 mil [THT]"]
  U4 = LM317

nets:
  5V: Componente2.5V, S1.Pin_3, S1.Pin_4, S2.Pin_3, S2.Pin_4, S3.Pin_3, S3.Pin_4, R1.Pin_0, R2.Pin_0, R3.Pin_0, C1.0, C2.+, Componente4.5V, U2.output_voltage, Q1.E, Q2.E, Q3.E, LED16.cathode, LED22.anode, LED23.cathode, LED24.cathode, LED25.cathode, LCM1602_IIC1.connector17, U4.connector2
  GND: Componente2.GND, C1.1, C2.-, Componente4.GND, Power_plug1.GND, U2.GND, LED1.cathode, R5.Pin_0, LED2.cathode, LED3.cathode, LED4.cathode, LED5.cathode, LED6.cathode, LED7.cathode, LED8.cathode, LED9.cathode, LED10.cathode, LED11.cathode, LED12.cathode, LED13.cathode, LED18.cathode, LCM1602_IIC1.connector16
  N1: Componente2.SCL, Componente4.SCL, LCM1602_IIC1.connector19
  N2: Componente2.SDA, Componente4.SDA, LCM1602_IIC1.connector18
  N3: S1.Pin_1, S1.Pin_2, R1.Pin_1, Componente4.D8_PWM
  N4: S2.Pin_1, S2.Pin_2, R3.Pin_1, Componente4.D7_PWM
  N5: S3.Pin_1, S3.Pin_2, R2.Pin_1, Componente4.D6_PWM
  N6: LCD1.VSS, LCM1602_IIC1.connector0
  N7: LCD1.VDD, LCM1602_IIC1.connector1
  N8: LCD1.V0, LCM1602_IIC1.connector2
  N9: LCD1.RS, LCM1602_IIC1.connector3
  N10: LCD1.R/W, LCM1602_IIC1.connector4
  N11: LCD1.E, LCM1602_IIC1.connector5
  N12: LCD1.DB0, LCM1602_IIC1.connector6
  N13: LCD1.DB1, LCM1602_IIC1.connector7
  N14: LCD1.DB2, LCM1602_IIC1.connector8
  N15: LCD1.DB3, LCM1602_IIC1.connector9
  N16: LCD1.DB4, LCM1602_IIC1.connector10
  N17: LCD1.DB5, LCM1602_IIC1.connector11
  N18: LCD1.DB6, LCM1602_IIC1.connector12
  N19: LCD1.DB7, LCM1602_IIC1.connector13
  N20: LCD1.LED+, LCM1602_IIC1.connector14
  N21: LCD1.LED-, LCM1602_IIC1.connector15
  N22: Componente4.D22, R25.Pin_1
  N23: Componente4.D23, R23.Pin_1
  N24: Componente4.D24, R24.Pin_1
  N25: Componente4.D25, R21.Pin_1
  N26: Componente4.D26, R22.Pin_1
  N27: Componente4.D27, R4.Pin_1
  N28: Componente4.D28, R7.Pin_1
  N29: Componente4.D29, R8.Pin_1
  N30: Componente4.D30, R9.Pin_1
  N31: Componente4.D31, R10.Pin_1
  N32: Componente4.D32, R11.Pin_1
  N33: Componente4.D33, R12.Pin_1
  N34: Componente4.D34, R13.Pin_1
  N35: Componente4.D35, R14.Pin_1
  N36: Componente4.D36, R15.Pin_1
  N37: Componente4.D37, R16.Pin_1
  N38: Componente4.D38, R17.Pin_1
  N39: Power_plug1.VCC, D2.anode
  N40: U2.input_voltage, D2.cathode
  N41: R4.Pin_0, LED1.anode
  N42: R5.Pin_1, R6.connector0, U4.connector0
  N43: R6.connector1, U4.connector1
  N44: R7.Pin_0, LED2.anode
  N45: R8.Pin_0, LED3.anode
  N46: R9.Pin_0, LED4.anode
  N47: R10.Pin_0, LED5.anode
  N48: R11.Pin_0, LED6.anode
  N49: R12.Pin_0, LED8.anode
  N50: R13.Pin_0, LED7.anode
  N51: R14.Pin_0, LED9.anode
  N52: R15.Pin_0, LED10.anode
  N53: R16.Pin_0, LED11.anode
  N54: R17.Pin_0, LED12.anode
  N55: Q1.B, R23.Pin_0
  N56: Q1.C, R20.Pin_0
  N57: Q2.B, R24.Pin_0
  N58: Q2.C, R26.Pin_0
  N59: Q3.B, R25.Pin_0
  N60: Q3.C, R19.Pin_0
  N61: R19.Pin_1, LED16.anode
  N62: R20.Pin_1, LED23.anode, LED24.anode
  N63: R21.Pin_0, LED18.anode
  N64: R22.Pin_0, LED13.anode
  N65: R26.Pin_1, LED25.anode
  N66: LCM1602_IIC1.connector20, LCM1602_IIC1.connector21

notes:
  5 V.
  3 V.
  Seconds
  Minutes
