# Fritzing sketch id1676_fichina_0 (saved by Fritzing 0.8.7b)
circuit board: 14.5061cm x 7.79213cm
breadboards: 1

parts:
  J1 = female pin header, 6 pins [form="♀ (female)"]
  J2 = female pin header, 6 pins [form="♀ (female)"]
  J3 = female pin header, 8 pins [form="♀ (female)"]
  J4 = female pin header, 8 pins [form="♀ (female)"]
  Power_plug1 = Power plug
  jumper = Toggle Switch [package=THT]
  1N4007 = Rectifier Diode [part_number=1N4007 package="300 mil [THT]"]
  22pF = Ceramic Capacitor [capacitance=100nF package="100 mil [THT, multilayer]"]
  22pF_2 = Ceramic Capacitor [capacitance=10pF package="100 mil [THT, multilayer]"]
  0_1uF = Ceramic Capacitor [capacitance=100nF package="200 mil [THT, multilayer]"]
  LED = LED - 3mm [color="Red (633nm)" package="3 mm [THT]"]
  1K = Resistor [tolerance=±5% resistance=1k package=THT]
  LED_2 = LED - 3mm [color="Red (633nm)" package="3 mm [THT]"]
  RST = Pushbutton [package="[THT]"]
  10K = Resistor [tolerance=±5% resistance=10k package=THT]
  1K_2 = Resistor [tolerance=±5% resistance=1k package=THT]
  100uF = Electrolytic Capacitor [capacitance=47µF voltage=20V package="100 mil [THT, electrolytic]"]
  100uF_2 = Electrolytic Capacitor [capacitance=47µF voltage=20V package="100 mil [THT, electrolytic]"]
  10nF = Ceramic Capacitor [capacitance=10nF package="100 mil [THT, multilayer]"]
  ATMEGA328P = atmega328 [part_number="ATMEGA 328" package=dip]
  16Mhz = Crystal [frequency="16 Mhz" package=THT]
  7805 = Voltage Regulator - 5V [package="TO220 [THT]"]
  JP1 = RCA [package=rca_lock]
  S6 = SWITCH-MOMENTARY-2 [package=tactile-pth-12mm]
  S7 = SWITCH-MOMENTARY-2 [package=tactile-pth-12mm]
  S8 = SWITCH-MOMENTARY-2 [package=tactile-pth-12mm]
  S9 = SWITCH-MOMENTARY-2 [package=tactile-pth-12mm]
  S10 = SWITCH-MOMENTARY-2 [package=tactile-pth-12mm]
  part = Rectifier Diode [part_number=1N4148 package="300 mil [THT]"]
  part_2 = Rectifier Diode [part_number=1N4148 package="300 mil [THT]"]
  part_3 = Resistor [tolerance=±5% resistance=1k package=THT]
  part_4 = Resistor [tolerance=±5% resistance=330 package=THT]
  R3 = Resistor [tolerance=±5% resistance=330 package=THT]
  part_5 = Resistor [tolerance=±5% resistance=10k package=THT]
  VIDEO = RCA [package=rca_lock]
  R5 = Resistor [tolerance=±5% resistance=68 package=THT]
  R7 = Rotary Potentiometer (Small) [maximum_resistance=100kΩ package=THT]
  R6 = Rotary Potentiometer (Small) [maximum_resistance=100kΩ package=THT]
  J6 = male pin header, 6 pins [form="♂ (male)"]

nets:
  N1: J1.pin1, ATMEGA328P.A5
  N2: J1.pin2, ATMEGA328P.A4
  N3: J1.pin3, ATMEGA328P.A3
  N4: J1.pin4, ATMEGA328P.A2
  N5: J1.pin5, ATMEGA328P.A1, R7.wiper
  N6: J1.pin6, ATMEGA328P.A0, R6.wiper
  N7: J2.pin1, 1N4007.cathode, 100uF_2.+, 7805.input_voltage
  GND: J2.pin2, J2.pin3, J4.pin7, Power_plug1.GND, 22pF.0, 22pF_2.1, 1K.Pin_0, RST.Pin_3, RST.Pin_4, 1K_2.Pin_1, 100uF.-, 100uF_2.-, 10nF.1, ATMEGA328P.GND, 7805.GND, JP1.SHELL, S6.1, S7.1, S8.1, S9.1, S10.2, part_5.Pin_1, VIDEO.SHELL, R5.Pin_1, R7.leg1, R6.leg1, J6.pin6
  N8: J2.pin4, jumper.COM, LED_2.anode, 10K.Pin_1, ATMEGA328P.VCC, ATMEGA328P.AVCC, R7.leg2, R6.leg2
  N9: J2.pin6, 0_1uF.1, J6.pin1
  N10: J3.pin1, ATMEGA328P.D0_(RX), J6.pin3
  N11: J3.pin2, ATMEGA328P.D1_(TX), J6.pin2
  N12: J3.pin3, ATMEGA328P.D2, S8.2
  N13: J3.pin4, ATMEGA328P.D3_(PWM), S9.2
  N14: J3.pin5, ATMEGA328P.D4, S6.2
  N15: J3.pin6, ATMEGA328P.D5_(PWM), S7.2
  N16: J3.pin7, ATMEGA328P.D6_(PWM)
  N17: J3.pin8, ATMEGA328P.D7, part.anode
  N18: J4.pin1, ATMEGA328P.D8
  N19: J4.pin2, ATMEGA328P.D9_(PWM), part_2.anode
  N20: J4.pin3, ATMEGA328P.D10_(PWM), S10.1
  N21: J4.pin4, ATMEGA328P.D11_(PWM), R3.Pin_1
  N22: J4.pin5, ATMEGA328P.D12, part_5.Pin_0
  N23: J4.pin6, LED.anode, ATMEGA328P.D13
  N24: J4.pin8, 10nF.0, ATMEGA328P.AREF
  N25: Power_plug1.VCC, 1N4007.anode
  N26: jumper.L1, J6.pin4
  N27: jumper.L2, 100uF.+, 7805.output_voltage
  N28: 22pF.1, ATMEGA328P.XLAT1, 16Mhz.pin_1
  N29: 22pF_2.0, ATMEGA328P.XLAT2, 16Mhz.pin_0
  N30: 0_1uF.0, RST.Pin_1, RST.Pin_2, 10K.Pin_0, ATMEGA328P.RESET
  N31: LED.cathode, 1K.Pin_1
  N32: LED_2.cathode, 1K_2.Pin_0
  N33: JP1.PIN, JP1.SWITCH, R3.Pin_0
  N34: part.cathode, part_4.Pin_1
  N35: part_2.cathode, part_3.Pin_1
  N36: part_3.Pin_0, part_4.Pin_0, VIDEO.PIN, VIDEO.SWITCH, R5.Pin_0

notes:
  2
  ~6
  (TX) 1
  4
  ~3
  7
  ~5
  (RX) 0
  12
  ~9
  ~10
  ~11
  8
  13
  GND
  AREF
  PWM~
  DIGITAL
  ANALOG
  3
  5
  1
  0
  USB
  EXT
  5V
  RX
  TX
  DTR
  RST
  Vin
  7/12V
  D2
  D5
  D4
  D3
  D10
  A1
  A0
  VIDEO
  AUDIO
  Uses TVout library
  laboratoriodejuguete.com
  HLQSTCEC
  by Myles Metzler
  based on HACKVISION
  by nootropicdesign.com
  FICHINA
  R5 (68 Ohm) is not necessary in most cases
  Arduino Shield compatible game console
  bY NOOTROPIC DESIGN
  nootropicdesign.com
  uses TV Out Library
  http://code.google.com/p/arduino-tvout/
