# Fritzing sketch id1677_FilamentConnector_0 (saved by Fritzing 0.9.2b)
circuit board: 8cm x 3.45351cm
breadboards: 1

parts:
  ATMEGA328P-PU2 = atmega328 [package=dip]
  XTAL1 = Crystal [frequency="16 Mhz" package=THT]
  C8 = Ceramic Capacitor [capacitance=100nF package="200 mil [THT, multilayer]"]
  C9 = Ceramic Capacitor [capacitance=100nF package="200 mil [THT, multilayer]"]
  C10 = Ceramic Capacitor [capacitance=22pF package="200 mil [THT, multilayer]"]
  C11 = Ceramic Capacitor [capacitance=22pF package="200 mil [THT, multilayer]"]
  R4 = Resistor [tolerance=±5% resistance=1k package=THT]
  R5 = Resistor [tolerance=±5% resistance=10k package=THT]
  LED1 = LED - 3mm [color="Green (555nm)" package="3 mm [THT]"]
  ABS = Pushbutton [package="[THT]"]
  PLA = Pushbutton [package="[THT]"]
  RESET = Pushbutton [package="[THT]"]
  R6 = Resistor [tolerance=±5% resistance=10k package=THT]
  R7 = Resistor [tolerance=±5% resistance=10k package=THT]
  R8 = Resistor [tolerance=±5% resistance=4.7k package=THT]
  R9 = Resistor [tolerance=±5% resistance=1k package=THT]
  LED2 = LED - 3mm [color="Green (555nm)" package="3 mm [THT]"]
  R10 = Resistor [tolerance=±5% resistance=1k package=THT]
  C12 = Electrolytic Capacitor [capacitance=1µF package="100 mil [THT, electrolytic]"]
  J3 = Screw terminal - 2 pins [package=THT]
  Q1 = npn-Powertransistor [package="TO220 [THT]"]
  U1 = Voltage Regulator - 5V [package="TO220 [THT]"]
  J2 = Screw terminal - 2 pins [package=THT]
  J1 = Screw terminal - 2 pins [package=THT]

nets:
  N1: ATMEGA328P-PU2.RESET, R5.Pin_1, RESET.Pin_3, RESET.Pin_4
  N2: ATMEGA328P-PU2.VCC, ATMEGA328P-PU2.AVCC, ATMEGA328P-PU2.AREF, C8.0, C9.1, R5.Pin_0, ABS.Pin_1, ABS.Pin_2, PLA.Pin_1, PLA.Pin_2, R8.Pin_1, C12.+, U1.output_voltage
  GND: ATMEGA328P-PU2.GND, C8.1, C9.0, C10.1, C11.1, R4.Pin_0, RESET.Pin_1, RESET.Pin_2, R6.Pin_0, R7.Pin_0, R9.Pin_0, R10.Pin_0, C12.-, J3.pin2, Q1.emitter, U1.GND, J1.pin1
  N3: ATMEGA328P-PU2.XLAT1, XTAL1.pin_1, C10.0
  N4: ATMEGA328P-PU2.XLAT2, XTAL1.pin_0, C11.0
  N5: ATMEGA328P-PU2.D5_(PWM), LED1.anode
  N6: ATMEGA328P-PU2.D6_(PWM), R9.Pin_1, LED2.anode, Q1.base
  N7: ATMEGA328P-PU2.D7, ABS.Pin_3, ABS.Pin_4, R7.Pin_1
  N8: ATMEGA328P-PU2.D8, PLA.Pin_3, PLA.Pin_4, R6.Pin_1
  N9: ATMEGA328P-PU2.A0, R8.Pin_0, J3.pin1
  N10: R4.Pin_1, LED1.cathode
  N11: LED2.cathode, R10.Pin_1
  N12: Q1.collector, J2.pin1
  N13: U1.input_voltage, J2.pin2, J1.pin2

notes:
  GND
  VIN
  V-
  HEATER
  TEMP
  Designed by Simon@Airfit.CN
