# Fritzing sketch id167_6_LEDs_0 (saved by Fritzing 0.9.3b)
circuit board: 10.5014cm x 7.83985cm
breadboards: 1

parts:
  Part1 = Arduino Uno (Rev3)
  R1 = Resistor [tolerance=±5% resistance=1k package=THT]
  LED_1 = LED - 5mm [color="Red (633nm)" package="5 mm [THT]"]
  LED_2 = LED - 5mm [color="Red (633nm)" package="5 mm [THT]"]
  LED_3 = LED - 5mm [color="Red (633nm)" package="5 mm [THT]"]
  LED_4 = LED - 5mm [color="Red (633nm)" package="5 mm [THT]"]
  LED_5 = LED - 5mm [color="Red (633nm)" package="5 mm [THT]"]
  LED_6 = LED - 5mm [color="Red (633nm)" package="5 mm [THT]"]

nets:
  N1: Part1.D8, LED_5.anode
  N2: Part1.D9_PWM, LED_4.anode
  N3: Part1.D10_PWM/SS, LED_3.anode
  N4: Part1.D11_PWM/MOSI, LED_2.anode
  N5: Part1.D12/MISO, LED_1.anode
  N6: Part1.GND, R1.Pin_0
  N7: Part1.D2, LED_6.anode
  N8: R1.Pin_1, LED_1.cathode, LED_2.cathode, LED_3.cathode, LED_4.cathode, LED_5.cathode, LED_6.cathode
