# Fritzing sketch id1682_Final_Lab_Challenge_0 (saved by Fritzing 0.9.3b)
breadboards: 2

parts:
  Part1 = Arduino Uno (Rev3)
  LCD1 = LCD screen
  R1 = TRIMPOT [package=3386u]
  hc-sr1 = hc-sr04
  T1 = LM35 Temperature Sensor [package="TO92 [THT]"]
  R2 = Basic Flex Resistor
  R3 = Resistor [tolerance=±5% resistance=10k package=THT]

nets:
  N1: Part1.A0, T1.Vout
  N2: Part1.A1, R2.Pin_2, R3.Pin_0
  N3: Part1.D9_PWM, hc-sr1.Echo
  N4: Part1.D10_PWM/SS, hc-sr1.Trig
  N5: Part1.D11_PWM/MOSI, LCD1.E
  N6: Part1.D12/MISO, LCD1.RS
  N7: Part1.D2, LCD1.DB7
  N8: Part1.D3_PWM, LCD1.DB6
  N9: Part1.D4, LCD1.DB5
  N10: Part1.D5_PWM, LCD1.DB4
  5V: Part1.5V, LCD1.VDD, LCD1.LED+, R1.CW, hc-sr1.VCC, T1.+Vs, R3.Pin_1
  GND: Part1.GND, LCD1.VSS, LCD1.R/W, LCD1.LED-, R1.CCW, hc-sr1.GND, T1.GND, R2.pin_1
  N11: LCD1.V0, R1.WIPER
