# Fritzing sketch id1683_ralph_0 (saved by Fritzing 0.9.3b)
breadboards: 1

parts:
  LED1 = LED - 5mm [color="Yellow (595nm)" package="5 mm [THT]"]
  LED2 = LED - 5mm [color="White (8000K)" package="5 mm [THT]"]
  LED3 = LED - 5mm [color="Green (555nm)" package="5 mm [THT]"]
  S1 = Pushbutton [package="[THT]"]
  Part1 = Arduino Uno (Rev3)
  S2 = Pushbutton [package="[THT]"]
  S3 = Pushbutton [package="[THT]"]
  R1 = Resistor [tolerance=±5% resistance=220 package=THT]
  R2 = Resistor [tolerance=±5% resistance=220 package=THT]
  R3 = Resistor [tolerance=±5% resistance=220 package=THT]

nets:
  N1: LED1.cathode, Part1.D12/MISO
  N2: LED1.anode, LED2.anode, LED3.anode, Part1.GND, R1.Pin_0, R2.Pin_0, R3.Pin_0
  N3: LED2.cathode, Part1.D11_PWM/MOSI
  N4: LED3.cathode, Part1.D13/SCK
  N5: S1.Pin_1, S1.Pin_2
  N6: S1.Pin_3, S1.Pin_4, Part1.D5_PWM, Part1.D6_PWM, Part1.D7, Part1.5V, S2.Pin_3, S2.Pin_4, S3.Pin_1, S3.Pin_2, R1.Pin_1, R2.Pin_1, R3.Pin_1
  N7: S2.Pin_1, S2.Pin_2
  N8: S3.Pin_3, S3.Pin_4
