# Fritzing sketch id1684_fingerino6_0 (saved by Fritzing 0.7.1b)
breadboards: 1

parts:
  Arduino1 = Arduino
  U1 = mystery part, 3 pins [chip_label=A1326 spacing=300mil]
  U2 = mystery part, 3 pins [chip_label=A1326 spacing=300mil]
  U3 = mystery part, 3 pins [chip_label=A1326 spacing=300mil]
  U4 = mystery part, 3 pins [chip_label=A1326 spacing=300mil]
  U5 = mystery part, 3 pins [chip_label=A1326 spacing=300mil]
  U6 = mystery part, 3 pins [chip_label=A1326 spacing=300mil]  # not connected
  R1 = Resistor [tolerance=±5% resistance=220 package=THT]
  R2 = Resistor [tolerance=±5% resistance=220 package=THT]

nets:
  N1: Arduino1.aref, R1.Pin_0, R2.Pin_1
  N2: Arduino1.+5V, U1.pin1, U2.pin1, U3.pin1, U4.pin1, U5.pin1, R1.Pin_1
  N3: Arduino1.GND, U1.pin2, U2.pin2, U3.pin2, U4.pin2, U5.pin2, R2.Pin_0
  N4: Arduino1.A0, U1.pin3
  N5: Arduino1.A1, U2.pin3
  N6: Arduino1.A2, U3.pin3
  N7: Arduino1.A3, U4.pin3
  N8: Arduino1.A4, U5.pin3
