# Fritzing sketch id1685_Fiona_ATS_0 (saved by Fritzing 0.9.2b)
breadboards: 1

parts:
  Part1 = Arduino Uno (Rev3)
  R1 = Resistor [tolerance=±5% resistance=560 package="1206 [SMD]"]
  R2 = Resistor [tolerance=±5% resistance=560 package="1206 [SMD]"]
  R4 = Resistor [tolerance=±5% resistance=560 package="1206 [SMD]"]
  R5 = Resistor [tolerance=±5% resistance=560 package="1206 [SMD]"]
  LED3 = smd LED [color="Yellow (585nm)" package="0805 [SMD]"]
  LED6 = smd LED [color="Green (555nm)" package="0805 [SMD]"]
  LED7 = smd LED [color="Blue (430nm)" package="0805 [SMD]"]
  LED8 = smd LED [color="Red (633nm)" package="0805 [SMD]"]
  R6 = PHOTOCELL [package=photocell-kit]
  R7 = Resistor [tolerance=±5% resistance=10k package="1206 [SMD]"]

nets:
  N1: Part1.A0, R6.P$1, R7.Pin_0
  N2: Part1.D2, LED6.anode
  N3: Part1.D4, LED3.anode
  N4: Part1.D6_PWM, LED7.anode
  N5: Part1.D7, LED8.anode
  N6: Part1.5V, R6.P$2
  N7: Part1.GND, R1.Pin_1, R4.Pin_1, R5.Pin_1, R7.Pin_1
  N8: R1.Pin_0, LED6.cathode
  N9: R2.Pin_0, LED3.cathode
  N10: R4.Pin_0, LED7.cathode
  N11: R5.Pin_0, LED8.cathode
