# Fritzing sketch id1687_fire_fither_0 (saved by Fritzing 0.9.3b)
breadboards: 1

parts:
  Part1 = Arduino Uno (Rev3) - ICSP
  S1 = prefix0000
  M1 = DC Motor
  M2 = DC Motor
  U1 = Vibration Motor- ROB-08449 [package=vibe-motor-10mm]
  IC1 = L293D [package=THT]

nets:
  N1: Part1.D9_PWM, S1.connector3
  N2: Part1.GND, S1.connector1, U1.+, IC1.0V, IC1.Enable_2
  N3: Part1.D2, IC1.In_3
  N4: Part1.D3_PWM, IC1.In_4
  N5: Part1.D4, IC1.In_2
  N6: Part1.D5_PWM, IC1.In_1
  N7: Part1.D6_PWM, U1.-
  N8: Part1.5V, S1.connector0, IC1.Enable_1, IC1.+V
  N9: Part1.VIN, IC1.+Vmotor
  N10: M1.pin_1, IC1.Out_2_(_Controlled_by_Enable_1_)
  N11: M1.pin_2, IC1.Out_1_(_Controlled_by_Enable_1_)
  N12: M2.pin_1, IC1.Out_4_(_Controlled_by_Enable_2_)
  N13: M2.pin_2, IC1.Out_3_(_Controlled_by_Enable_2_)

notes:
  FIRE FITHTING ROBOT
  Water Pump Module
