# Fritzing sketch id1689_EDSP5_Assingment3 (saved by Fritzing 0.9.3b)
breadboards: 1

parts:
  KEYPAD1 = Membrane_Matrix_Keypad
  Part1 = Arduino Uno (Rev3) - ICSP
  J1 = Piezo Speaker
  LED1 = smd LED [color="Red (633nm)" package="0603 [SMD]"]
  R1 = Resistor [tolerance=±5% resistance=220 package="0402 [SMD]"]
  M1 = Dagu DGServo 9g (Top view) [part_number=RS001B]
  Q1 = PNP-Transistor [package="TO92 [THT]"]
  R2 = Resistor [tolerance=±5% resistance=1k package="0402 [SMD]"]

nets:
  N1: KEYPAD1.connector1, Part1.D7
  N2: KEYPAD1.connector2, Part1.D8
  N3: KEYPAD1.connector3, Part1.D9_PWM
  N4: KEYPAD1.connector4, Part1.D10_PWM/SS
  N5: KEYPAD1.connector5, Part1.D3_PWM
  N6: KEYPAD1.connector6, Part1.D4
  N7: KEYPAD1.connector7, Part1.D6_PWM
  N8: Part1.ICSP_MOSI, Part1.D11_PWM/MOSI, M1.gnd
  N9: Part1.D1/TX, R2.Pin_1
  N10: Part1.D5_PWM, LED1.anode
  N11: J1.pin1, M1.vcc
  N12: J1.pin2, Q1.C
  N13: LED1.cathode, R1.Pin_0
  N14: R1.Pin_1, M1.pulse, Q1.E
  N15: Q1.B, R2.Pin_0
