# Fritzing sketch id1689_Test_555_0 (saved by Fritzing 0.9.3b)
circuit board: 3.58132cm x 2.64955cm
breadboards: 1

parts:
  U1 = 555 Timer [package="DIP8 [THT]"]
  R1 = Resistor [tolerance=±5% resistance=1k package=THT]
  R2 = Resistor [tolerance=±5% resistance=470k package=THT]
  VCC1 = Battery block 9V
  C1 = Electrolytic Capacitor [capacitance=10µF package="100 mil [THT, electrolytic]"]
  R3 = Resistor [tolerance=±5% resistance=1k package=THT]
  LED1 = LED - 5mm [color="Red (633nm)" package="5 mm [THT]"]

nets:
  N1: U1.Ground, U1.Reset, U1.Vcc_Supply_Voltage, R1.Pin_0, VCC1.-, VCC1.+, C1.-, LED1.cathode
  N2: U1.Trigger, U1.Threshold, R2.Pin_1, C1.+
  N3: U1.Output, R3.Pin_0
  N4: U1.Discharge, R1.Pin_1, R2.Pin_0
  N5: R3.Pin_1, LED1.anode
