# Fritzing sketch id1690_Temp_Start_0 (saved by Fritzing 0.9.0b)
breadboards: 1

parts:
  BeagleBone1 = BeagleBone_Black
  R1 = Resistor [tolerance=±5% resistance=1k package=THT]
  C1 = Ceramic Capacitor [capacitance=100nF package="100 mil [THT, multilayer]"]

nets:
  N1: BeagleBone1.connector32, C1.1
  N2: BeagleBone1.connector34, R1.Pin_0
  N3: BeagleBone1.connector36, R1.Pin_1, C1.0
