# Fritzing sketch id1691_frankk_0 (saved by Fritzing 0.9.2b)
breadboards: 1

parts:
  J1 = Basic Servo
  J2 = Basic Servo
  J3 = Basic Servo
  J4 = Basic Servo
  J5 = Basic Servo
  Part1 = Arduino Mega 2560 (Rev3)
  S1 = Pushbutton [package="[SMD]"]
  R1 = Resistor [tolerance=±5% resistance=100k package="2512 [SMD]"]
  U1 = POT [package=pot_alpha_rv16af-20]

nets:
  GND: J1.gnd, J2.gnd, J3.gnd, J4.gnd, J5.gnd, Part1.GND, R1.Pin_1, U1.A
  VCC: J1.vcc, J2.vcc, J3.vcc, J4.vcc, J5.vcc
  N1: J1.pulse, Part1.D5_PWM
  N2: J2.pulse, Part1.D4_PWM
  N3: J3.pulse, Part1.D6_PWM
  N4: J4.pulse, Part1.D8_PWM
  N5: J5.pulse, Part1.D7_PWM
  N6: Part1.5V, S1.Pin_3, S1.Pin_4, U1.E
  N7: Part1.D2_PWM, S1.Pin_1, S1.Pin_2, R1.Pin_0
  N8: Part1.D3_PWM, U1.S
