# Fritzing sketch id1692_Chris'sSchematic_0 (saved by Fritzing 0.9.0b)
breadboards: 1

parts:
  Part1 = Arduino Uno (Rev3)
  R1 = Resistor [tolerance=±5% resistance=220 package=THT]
  S1 = Pushbutton [package="[THT]"]
  LED1 = LED - 5mm [color="Red (633nm)" package="5 mm [THT]"]
  R3 = Resistor [tolerance=±5% resistance=220 package=THT]
  LED2 = LED - 5mm [color="Green (555nm)" package="5 mm [THT]"]
  R2 = Resistor [tolerance=±5% resistance=220 package=THT]

nets:
  N1: Part1.D2, R2.Pin_0
  N2: Part1.D7, R3.Pin_1
  N3: Part1.5V, R1.Pin_0
  N4: Part1.GND, LED1.cathode, LED2.cathode
  N5: S1.Pin_1, S1.Pin_2
  N6: S1.Pin_3, S1.Pin_4
  N7: LED1.anode, R2.Pin_1
  N8: R3.Pin_0, LED2.anode
