# Fritzing sketch id1693_PCB_0 (saved by Fritzing 0.9.3b)
circuit board: 8.46667cm x 5.64444cm
breadboards: 1

parts:
  U2 = ESP8266_module [part_number=ESP8266]
  Part1 = Arduino Uno (Rev3)
  11 = Resistor [tolerance=±5% resistance=1k package=THT]
  13 = Resistor [tolerance=±5% resistance=1k package=THT]
  4 = Resistor [tolerance=±5% resistance=1k package=THT]
  9 = Resistor [tolerance=±5% resistance=1k package=THT]
  10 = Resistor [tolerance=±5% resistance=1k package=THT]
  D/C = Resistor [tolerance=±5% resistance=2k package=THT]
  RESET = Resistor [tolerance=±5% resistance=2k package=THT]
  CS = Resistor [tolerance=±5% resistance=2k package=THT]
  MOSI = Resistor [tolerance=±5% resistance=2k package=THT]
  SCK = Resistor [tolerance=±5% resistance=2k package=THT]
  BAT1 = BC9VPC [package=bc9vpc]
  U3 = SWITCH_SPDT [package=kps-1290]
  FC-1 = sound sensor
  Part2 = adafruit [part_number="Adafruit #2090"]

nets (from the schematic view):
  N1: U2.connector0, Part1.D1/TX
  N2: U2.connector1, Part1.3V3
  N3: U2.connector6, Part1.GND, D/C.Pin_1, RESET.Pin_1, CS.Pin_1, MOSI.Pin_1, SCK.Pin_1, BAT1.V-, FC-1.connector9, Part2.connector30
  N4: U2.connector7, Part1.D0/RX
  N5: Part1.A0, FC-1.connector10
  N6: Part1.D8, Part2.connector34
  N7: Part1.D9_PWM, 9.Pin_0
  N8: Part1.D10_PWM/SS, 10.Pin_0
  N9: Part1.D11_PWM/MOSI, 11.Pin_0
  N10: Part1.D13/SCK, 13.Pin_0
  N11: Part1.D2, Part2.connector31
  N12: Part1.D4, 4.Pin_0
  N13: Part1.D5_PWM, Part2.connector33
  N14: Part1.D6_PWM, Part2.connector35
  N15: Part1.D7, Part2.connector36
  N16: Part1.5V, FC-1.connector8, Part2.connector21
  N17: Part1.VIN, U3.O
  N18: 11.Pin_1, MOSI.Pin_0, Part2.connector25
  N19: 13.Pin_1, SCK.Pin_0, Part2.connector3
  N20: 4.Pin_1, D/C.Pin_0, Part2.connector4
  N21: 9.Pin_1, RESET.Pin_0, Part2.connector28
  N22: 10.Pin_1, CS.Pin_0, Part2.connector26
  N23: BAT1.V+, U3.P

notes:
  3.3V
