# Fritzing sketch id1694_robo_tx_demo_0 (saved by Fritzing 0.8.7b)
breadboards: 1

parts:
  VCC1 = Battery block 9V
  Bauteil1 = prefix00ftrobotxv8
  M1 = DC Motor
  M2 = DC Motor
  R1 = Rotary Potentiometer (Small) [maximum_resistance=10kΩ package=THT]
  R2 = Photocell (LDR) [package=THT]
  LED1 = LED - 5mm [color="Red (633nm)" package="5 mm [THT]"]
  LED2 = LED - 5mm [color="Green (555nm)" package="5 mm [THT]"]
  R3 = Resistor [tolerance=±5% resistance=680k package=THT]
  R4 = Resistor [tolerance=±5% resistance=680 package=THT]
  U1 = DS1307 [package=so08]
  S1 = Round Pushbutton  # not connected

nets:
  N1: VCC1.-, Bauteil1.connector36
  N2: VCC1.+, Bauteil1.connector35
  N3: Bauteil1.connector0, R1.wiper
  N4: Bauteil1.connector5, R2.pin_0
  N5: Bauteil1.connector9, R1.leg1
  N6: Bauteil1.connector13, R2.pin_1
  N7: Bauteil1.connector17, M1.pin_1
  N8: Bauteil1.connector18, M2.pin_1
  N9: Bauteil1.connector19, LED1.cathode
  N10: Bauteil1.connector21, M1.pin_2
  N11: Bauteil1.connector22, M2.pin_2
  N12: Bauteil1.connector23, LED2.cathode
  N13: Bauteil1.connector28, R3.Pin_1, R4.Pin_1, U1.GND
  N14: Bauteil1.connector34, R1.leg2
  N15: Bauteil1.connector43, U1.SCL
  N16: Bauteil1.connector44, U1.SDA
  N17: Bauteil1.connector47, U1.VCC
  N18: LED1.anode, R3.Pin_0
  N19: LED2.anode, R4.Pin_0
