# Fritzing sketch id1695_fishled_0 (saved by Fritzing 0.9.2b)
breadboards: 1

parts:
  S1 = Pushbutton [package="[THT]"]
  元件1 = Arduino Uno (Rev3)
  LED1 = LED - 3mm [color="Red (633nm)" package="3 mm [THT]"]
  LED2 = LED - 3mm [color="White (6500K)" package="3 mm [THT]"]
  LED3 = LED - 3mm [color="Red (633nm)" package="3 mm [THT]"]
  R1 = Resistor [tolerance=±5% resistance=220 package=THT]
  R2 = Resistor [tolerance=±5% resistance=220 package=THT]
  R3 = Resistor [tolerance=±5% resistance=220 package=THT]
  R4 = Resistor [tolerance=±5% resistance=220 package=THT]

nets:
  N1: S1.Pin_1, S1.Pin_2, 元件1.D8, R4.Pin_0
  N2: S1.Pin_3, S1.Pin_4, 元件1.5V
  N3: 元件1.D2, R3.Pin_1
  N4: 元件1.D3_PWM, R2.Pin_1
  N5: 元件1.D4, R1.Pin_1
  N6: 元件1.GND, LED1.cathode, LED2.cathode, LED3.cathode, R4.Pin_1
  N7: LED1.anode, R1.Pin_0
  N8: LED2.anode, R2.Pin_0
  N9: LED3.anode, R3.Pin_0
