# Fritzing sketch id1696_fish_tank_0 (saved by Fritzing 0.9.3b)
breadboards: 1

parts:
  Raspberry_Pi_1 = Raspberry Pi 3 [part_number=RPI-3-V1.2]
  U1 = 4ChannelRelay

nets:
  N1: Raspberry_Pi_1.GND, U1.connector1
  N2: Raspberry_Pi_1.GIPO24, U1.connector3
  N3: Raspberry_Pi_1.GIPO23, U1.connector2
  N4: Raspberry_Pi_1.5V, U1.connector10
