# Fritzing sketch id1698_munsflash_0 (saved by Fritzing 0.9.0b)
circuit board: 3.1cm x 2.9cm
breadboards: 1

parts:
  green = LED - 5mm [color="Red (633nm)" package="5 mm [THT]"]
  1k_Ω = Resistor [tolerance=±5% resistance=1k package=THT]
  1k_Ω_2 = Resistor [tolerance=±5% resistance=1k package=THT]
  330Ω = Resistor [tolerance=±5% resistance=330 package=THT]
  330Ω_2 = Resistor [tolerance=±5% resistance=330 package=THT]
  red = LED - 5mm [color="Green (555nm)" package="5 mm [THT]"]
  E_B_C = NPN-Transistor [package="TO92 [THT]"]
  C2 = Ceramic Capacitor [capacitance=100nF package="100 mil [THT, multilayer]"]
  C1 = Ceramic Capacitor [capacitance=100nF package="100 mil [THT, multilayer]"]
  E_B_C_2 = NPN-Transistor [package="TO92 [THT]"]
  -_+_9V = Battery block 9V
  J1 = female pin header, 2 pins [form="♀ (female)"]

nets (from the pcb view):
  N1: green.cathode, 330Ω_2.Pin_0
  N2: green.anode, 1k_Ω.Pin_0, 1k_Ω_2.Pin_0, red.anode, -_+_9V.+
  N3: 1k_Ω.Pin_1, E_B_C.B, C1.0
  N4: 1k_Ω_2.Pin_1, C2.1, E_B_C_2.B
  N5: 330Ω.Pin_0, red.cathode
  N6: 330Ω.Pin_1, C1.1, E_B_C_2.C
  N7: 330Ω_2.Pin_1, E_B_C.C, C2.0
  N8: E_B_C.E, E_B_C_2.E, J1.pin2
  N9: -_+_9V.-, J1.pin1

notes:
  speaker
  Flashy leds
  (C) munsking
  Licenced under
  GPL V3.0
