# Fritzing sketch id1699_sensor_0 (saved by Fritzing 0.9.3b)
breadboards: 1

parts:
  R1 = Basic Flex Resistor
  R2 = Basic Flex Resistor
  R3 = Basic Flex Resistor
  R4 = Basic Flex Resistor
  R5 = Resistor [tolerance=±5% resistance=220 package=THT]
  R6 = Resistor [tolerance=±5% resistance=220 package=THT]
  R7 = Resistor [tolerance=±5% resistance=220 package=THT]
  R8 = Resistor [tolerance=±5% resistance=220 package=THT]
  Part1 = Arduino Uno (Rev3)

nets:
  N1: R1.Pin_2, R2.Pin_2, R3.Pin_2, R4.Pin_2, Part1.5V
  N2: R1.pin_1, R7.Pin_1, Part1.A3
  N3: R2.pin_1, R8.Pin_1, Part1.A2
  N4: R3.pin_1, R5.Pin_1, Part1.A0
  N5: R4.pin_1, R6.Pin_1, Part1.A1
  N6: R5.Pin_0, R6.Pin_0, R7.Pin_0, R8.Pin_0, Part1.GND
