# Fritzing sketch id1700_flex_sensor_via_digital_pin_0 (saved by Fritzing 0.9.2b)
breadboards: 1

parts:
  Part1 = Arduino Uno (Rev3)
  R1 = Resistor [tolerance=±5% resistance=1k package=THT]
  C1 = Ceramic Capacitor [capacitance=0.1µF package="100 mil [THT, multilayer]"]
  R2 = Basic Flex Resistor

nets:
  N1: Part1.D8, R1.Pin_0
  N2: Part1.5V, C1.1
  N3: Part1.GND, R2.Pin_2
  N4: R1.Pin_1, C1.0, R2.pin_1
