# Fritzing sketch id1701_Flexible_Linear_Actuator_Lock_Security_0 (saved by Fritzing 0.9.3b)

parts:
  V1 = DC Power [voltage=5]
  U1 = RELAY [package=relay-jzc]
  Part1 = Arduino Uno (Rev3) - ICSP
  Part2 = Bluetooth HC-05 Macho
  VCC4 = 4 x AAA Battery Mount  # not connected
  VCC3 = 4 x AAA Battery Mount  # not connected
  VCC6 = 4 x AAA Battery Mount  # not connected
  VCC5 = 4 x AAA Battery Mount  # not connected
  VCC7 = 4 x AAA Battery Mount  # not connected
  L1 = Solenoid  # not connected
  U3 = RELAY [package=relay-jzc]

nets:
  N1: V1.V+, Part1.3V3
  GND: V1.V-, U1.NO, Part1.GND, Part2.GND, U3.NO
  N2: U1.COIL2, Part1.D7
  N3: Part1.D0/RX, Part2.TXD
  N4: Part1.D1/TX, Part2.RXD
  N5: Part1.D6_PWM, U3.COIL2
  5V: Part1.5V, Part2.VCC
