# Fritzing sketch id1702_custom_iScan_0 (saved by Fritzing 0.9.2b)
circuit board: 8.46667cm x 5.64444cm
breadboards: 1

parts:
  부품1 = Arduino Uno (Rev3)
  R1 = Resistor [tolerance=±5% resistance=10k package=THT]
  J1 = Basic Force Sensing Resistor (FSR) [package=THT]
  J2 = Basic Force Sensing Resistor (FSR) [package=THT]
  R2 = Resistor [tolerance=±5% resistance=10k package=THT]
  U3 = LCD-16X2 [package=lcd-16x2_noholes]
  BAT1 = BC9VPC [package=bc9vpc]
  J3 = Basic Force Sensing Resistor (FSR) [package=THT]
  R3 = Resistor [tolerance=±5% resistance=10k package=THT]

nets:
  N1: 부품1.A0, 부품1.A1, R1.Pin_1, J1.pin_0, J2.pin_0, R2.Pin_1
  GND: 부품1.GND, R1.Pin_0, R2.Pin_0, U3.VSS, BAT1.V-, R3.Pin_0
  N2: 부품1.D1/TX, U3.R_W
  N3: 부품1.5V, J1.pin_1, J2.pin_1, U3.VO, BAT1.V+
  N4: J3.pin_0, R3.Pin_1
