# Fritzing sketch id1704_TIIIIIINY_FC_0 (saved by Fritzing 0.9.1b)
circuit board: 3.38189cm x 3.86922cm

parts:
  Part1 = Arduino Pro Mini v13
  J1 = female pin header, 6 pins [form="♀ (female)"]
  J2 = female pin header, 2 pins [form="♀ (female)"]
  J3 = female pin header, 6 pins [form="♀ (female)"]
  J4 = female pin header, 2 pins [form="♀ (female)"]
  J5 = female pin header, 6 pins [form="♀ (female)"]
  J6 = female pin header, 2 pins [form="♀ (female)"]
  J7 = female pin header, 6 pins [form="♀ (female)"]
  J8 = female pin header, 6 pins [form="♀ (female)"]
  J9 = female pin header, 6 pins [form="♀ (female)"]
  J10 = female pin header, 2 pins [form="♀ (female)"]
  J11 = female pin header, 2 pins [form="♀ (female)"]
  J12 = female pin header, 2 pins [form="♀ (female)"]
  J13 = female pin header, 2 pins [form="♀ (female)"]
  J14 = female pin header, 2 pins [form="♀ (female)"]
  J15 = female pin header, 2 pins [form="♀ (female)"]
  Part2 = IMU Digital Combo Board 6DOF  # not connected

nets:
  N1: Part1.A4, J10.pin2
  N2: Part1.A5, J10.pin1
  N3: Part1.GND, J5.pin6, J6.pin1, J11.pin1
  N4: Part1.VCC, J3.pin6, J4.pin1, J11.pin2
  N5: Part1.A3, J2.pin1
  N6: Part1.A2, J2.pin2
  N7: Part1.A1, J1.pin1
  N8: Part1.A0, J1.pin2
  N9: Part1.D13/SCK, J1.pin3
  N10: Part1.D12/MISO, J1.pin4
  N11: Part1.D11_PWM/MOSI, J1.pin5
  N12: Part1.D10_PWM/SS, J1.pin6
  N13: Part1.D9_PWM, J7.pin6
  N14: Part1.D8, J7.pin5
  N15: Part1.D7, J7.pin4
  N16: Part1.D6_PWM, J7.pin3
  N17: Part1.D5_PWM, J7.pin2
  N18: Part1.D4, J7.pin1
  N19: Part1.D3_PWM, J12.pin2
  N20: Part1.D2, J12.pin1
  N21: Part1.D1/RX, J15.pin2
  N22: Part1.D0/TX, J15.pin1
  N23: J8.pin1, J8.pin6, J13.pin1
  N24: J9.pin1, J9.pin6, J14.pin1

notes:
  tiny fc
