# Fritzing sketch id1706_flipper_0 (saved by Fritzing 0.6.3b)
breadboards: 7

parts:
  Teensy++1 = Teensy++ 2.0
  Switch1 = Pushbutton_Omron_B3F_4050_handgemacht [part_number="b3f-4050, b3f5050, b3f-4055, b3f-5051"]
  Switch2 = Pushbutton_Omron_B3F_4050_handgemacht [part_number="b3f-4050, b3f5050, b3f-4055, b3f-5051"]
  Switch3 = Pushbutton_Omron_B3F_4050_handgemacht [part_number="b3f-4050, b3f5050, b3f-4055, b3f-5051"]
  Switch4 = Pushbutton_Omron_B3F_4050_handgemacht [part_number="b3f-4050, b3f5050, b3f-4055, b3f-5051"]
  Switch5 = Pushbutton_Omron_B3F_4050_handgemacht [part_number="b3f-4050, b3f5050, b3f-4055, b3f-5051"]
  Switch6 = Pushbutton_Omron_B3F_4050_handgemacht [part_number="b3f-4050, b3f5050, b3f-4055, b3f-5051"]
  D1 = Rectifier Diode [part_number=1N4001 package="300 mil [THT]"]
  D2 = Rectifier Diode [part_number=1N4001 package="300 mil [THT]"]
  D3 = Rectifier Diode [part_number=1N4001 package="300 mil [THT]"]
  D4 = Rectifier Diode [part_number=1N4001 package="300 mil [THT]"]
  D5 = Rectifier Diode [part_number=1N4001 package="300 mil [THT]"]
  D6 = Rectifier Diode [part_number=1N4001 package="300 mil [THT]"]
  Switch7 = Pushbutton_Omron_B3F_4050_handgemacht [part_number="b3f-4050, b3f5050, b3f-4055, b3f-5051"]
  Switch8 = Pushbutton_Omron_B3F_4050_handgemacht [part_number="b3f-4050, b3f5050, b3f-4055, b3f-5051"]
  Switch9 = Pushbutton_Omron_B3F_4050_handgemacht [part_number="b3f-4050, b3f5050, b3f-4055, b3f-5051"]
  D7 = Rectifier Diode [part_number=1N4001 package="300 mil [THT]"]
  D8 = Rectifier Diode [part_number=1N4001 package="300 mil [THT]"]
  D9 = Rectifier Diode [part_number=1N4001 package="300 mil [THT]"]
  Switch10 = Pushbutton_Omron_B3F_4050_handgemacht [part_number="b3f-4050, b3f5050, b3f-4055, b3f-5051"]
  Switch11 = Pushbutton_Omron_B3F_4050_handgemacht [part_number="b3f-4050, b3f5050, b3f-4055, b3f-5051"]
  Switch12 = Pushbutton_Omron_B3F_4050_handgemacht [part_number="b3f-4050, b3f5050, b3f-4055, b3f-5051"]
  D10 = Rectifier Diode [part_number=1N4001 package="300 mil [THT]"]
  D11 = Rectifier Diode [part_number=1N4001 package="300 mil [THT]"]
  D12 = Rectifier Diode [part_number=1N4001 package="300 mil [THT]"]
  Switch13 = Pushbutton_Omron_B3F_4050_handgemacht [part_number="b3f-4050, b3f5050, b3f-4055, b3f-5051"]
  D13 = Rectifier Diode [part_number=1N4001 package="300 mil [THT]"]
  Switch14 = Pushbutton_Omron_B3F_4050_handgemacht [part_number="b3f-4050, b3f5050, b3f-4055, b3f-5051"]
  Switch15 = Pushbutton_Omron_B3F_4050_handgemacht [part_number="b3f-4050, b3f5050, b3f-4055, b3f-5051"]
  Switch16 = Pushbutton_Omron_B3F_4050_handgemacht [part_number="b3f-4050, b3f5050, b3f-4055, b3f-5051"]
  Switch17 = Pushbutton_Omron_B3F_4050_handgemacht [part_number="b3f-4050, b3f5050, b3f-4055, b3f-5051"]
  Switch18 = Pushbutton_Omron_B3F_4050_handgemacht [part_number="b3f-4050, b3f5050, b3f-4055, b3f-5051"]
  Switch19 = Pushbutton_Omron_B3F_4050_handgemacht [part_number="b3f-4050, b3f5050, b3f-4055, b3f-5051"]
  D14 = Rectifier Diode [part_number=1N4001 package="300 mil [THT]"]
  D15 = Rectifier Diode [part_number=1N4001 package="300 mil [THT]"]
  D16 = Rectifier Diode [part_number=1N4001 package="300 mil [THT]"]
  D17 = Rectifier Diode [part_number=1N4001 package="300 mil [THT]"]
  D18 = Rectifier Diode [part_number=1N4001 package="300 mil [THT]"]
  D19 = Rectifier Diode [part_number=1N4001 package="300 mil [THT]"]
  Switch20 = Pushbutton_Omron_B3F_4050_handgemacht [part_number="b3f-4050, b3f5050, b3f-4055, b3f-5051"]
  Switch21 = Pushbutton_Omron_B3F_4050_handgemacht [part_number="b3f-4050, b3f5050, b3f-4055, b3f-5051"]
  Switch22 = Pushbutton_Omron_B3F_4050_handgemacht [part_number="b3f-4050, b3f5050, b3f-4055, b3f-5051"]
  D20 = Rectifier Diode [part_number=1N4001 package="300 mil [THT]"]
  D21 = Rectifier Diode [part_number=1N4001 package="300 mil [THT]"]
  D22 = Rectifier Diode [part_number=1N4001 package="300 mil [THT]"]
  Switch23 = Pushbutton_Omron_B3F_4050_handgemacht [part_number="b3f-4050, b3f5050, b3f-4055, b3f-5051"]
  Switch24 = Pushbutton_Omron_B3F_4050_handgemacht [part_number="b3f-4050, b3f5050, b3f-4055, b3f-5051"]
  Switch25 = Pushbutton_Omron_B3F_4050_handgemacht [part_number="b3f-4050, b3f5050, b3f-4055, b3f-5051"]
  D23 = Rectifier Diode [part_number=1N4001 package="300 mil [THT]"]
  D24 = Rectifier Diode [part_number=1N4001 package="300 mil [THT]"]
  D25 = Rectifier Diode [part_number=1N4001 package="300 mil [THT]"]
  Switch26 = Pushbutton_Omron_B3F_4050_handgemacht [part_number="b3f-4050, b3f5050, b3f-4055, b3f-5051"]
  D26 = Rectifier Diode [part_number=1N4001 package="300 mil [THT]"]
  LED1 = LED_3mm_Bicolor_red_green_common_cathode_handgemacht
  LED2 = LED_3mm_Bicolor_red_green_common_cathode_handgemacht
  LED3 = LED_3mm_Bicolor_red_green_common_cathode_handgemacht
  LED4 = LED_3mm_Bicolor_red_green_common_cathode_handgemacht
  LED5 = LED_3mm_Bicolor_red_green_common_cathode_handgemacht
  LED6 = LED_3mm_Bicolor_red_green_common_cathode_handgemacht
  LED7 = LED_3mm_Bicolor_red_green_common_cathode_handgemacht
  LED8 = LED_3mm_Bicolor_red_green_common_cathode_handgemacht
  LED9 = LED_3mm_Bicolor_red_green_common_cathode_handgemacht
  R1 = Resistor [tolerance=±5% resistance=180 package=THT]
  R2 = Resistor [tolerance=±5% resistance=180 package=THT]
  R3 = Resistor [tolerance=±5% resistance=180 package=THT]
  R4 = Resistor [tolerance=±5% resistance=180 package=THT]
  R5 = Resistor [tolerance=±5% resistance=180 package=THT]
  R6 = Resistor [tolerance=±5% resistance=180 package=THT]
  R8 = Resistor [tolerance=±5% resistance=180 package=THT]
  R9 = Resistor [tolerance=±5% resistance=180 package=THT]
  R10 = Resistor [tolerance=±5% resistance=180 package=THT]
  R11 = Resistor [tolerance=±5% resistance=180 package=THT]
  R12 = Resistor [tolerance=±5% resistance=180 package=THT]
  R13 = Resistor [tolerance=±5% resistance=180 package=THT]
  R14 = Resistor [tolerance=±5% resistance=180 package=THT]
  R16 = Resistor [tolerance=±5% resistance=180 package=THT]
  R17 = Resistor [tolerance=±5% resistance=180 package=THT]
  R18 = Resistor [tolerance=±5% resistance=180 package=THT]
  R19 = Resistor [tolerance=±5% resistance=180 package=THT]
  R20 = Resistor [tolerance=±5% resistance=180 package=THT]
  S1 = Toggle Switch [package=THT]
  C1 = Ceramic Capacitor [capacitance=100nF package="100 mil [THT, multilayer]"]
  Q1 = NPN-Transistor [package="TO92 [THT]"]
  R22 = Resistor [tolerance=±5% resistance=1k package=THT]
  R23 = Resistor [tolerance=±5% resistance=9 package=THT]
  GLCD_128x1 = 128_x_64_Graphic_LCD
  VCC1 = Battery
  DC-DC1 = VPACK_PCB_5V_Stepup
  R21 = Rotary Potentiometer (Small) [maximum_resistance=100kΩ]
  R24 = Resistor [tolerance=±5% resistance=220 package=THT]
  J1 = Piezo Speaker

nets (from the pcb view):
  N1: Teensy++1.GND#0, LED1.connector1, LED2.connector1, LED3.connector1, LED4.connector1, LED5.connector1, LED6.connector1, LED7.connector1, LED8.connector1, LED9.connector1, GLCD_128x1.connector0, GLCD_128x1.connector19, VCC1.connector0, DC-DC1.connector2, R21.leg2, J1.pin1
  N2: Teensy++1.B7, R22.Pin_0
  N3: Teensy++1.D0, R9.Pin_1
  N4: Teensy++1.D1, R13.Pin_1
  N5: Teensy++1.D2, R11.Pin_1
  N6: Teensy++1.D3, R8.Pin_1
  N7: Teensy++1.D4, R5.Pin_1
  N8: Teensy++1.D5, R6.Pin_1
  N9: Teensy++1.D6, R3.Pin_1
  N10: Teensy++1.D7, R4.Pin_1
  N11: Teensy++1.E0, Switch1.connector1, Switch4.connector1, Switch7.connector1, Switch10.connector1
  N12: Teensy++1.E1, Switch2.connector1, Switch5.connector1, Switch8.connector1, Switch11.connector1
  N13: Teensy++1.C0, GLCD_128x1.connector6
  N14: Teensy++1.C1, GLCD_128x1.connector7
  N15: Teensy++1.C2, GLCD_128x1.connector8
  N16: Teensy++1.C3, GLCD_128x1.connector9
  N17: Teensy++1.C4, GLCD_128x1.connector10
  N18: Teensy++1.C5, GLCD_128x1.connector11
  N19: Teensy++1.C6, GLCD_128x1.connector12
  N20: Teensy++1.C7, GLCD_128x1.connector13
  N21: Teensy++1.VCC, Q1.C, GLCD_128x1.connector1, GLCD_128x1.connector16, DC-DC1.connector1
  N22: Teensy++1.F7, R24.Pin_1
  N23: Teensy++1.F6, Switch15.connector2, Switch18.connector2, Switch21.connector2, Switch24.connector2
  N24: Teensy++1.F5, D13.anode, D26.anode
  N25: Teensy++1.F4, D7.anode, D8.anode, D9.anode, D20.anode, D21.anode, D22.anode
  N26: Teensy++1.F3, D4.anode, D5.anode, D6.anode, D17.anode, D18.anode, D19.anode
  N27: Teensy++1.F2, D1.anode, D2.anode, D3.anode, D14.anode, D15.anode, D16.anode
  N28: Teensy++1.AREF, C1.1
  N29: Teensy++1.GND#32, C1.0
  N30: Teensy++1.E6, Switch3.connector1, Switch6.connector1, Switch9.connector1, Switch12.connector1, Switch13.connector1
  N31: Teensy++1.E7, R20.Pin_1
  N32: Teensy++1.B0, R17.Pin_1
  N33: Teensy++1.B1, R16.Pin_1
  N34: Teensy++1.B2, R18.Pin_1
  N35: Teensy++1.B3, R19.Pin_1
  N36: Teensy++1.B4, R12.Pin_1
  N37: Teensy++1.B5, R10.Pin_1
  N38: Teensy++1.B6, R14.Pin_1
  N39: Teensy++1.E4, R1.Pin_1
  N40: Teensy++1.E5, R2.Pin_1
  N41: Teensy++1.PA0, GLCD_128x1.connector15
  N42: Teensy++1.PA1, D10.anode, D11.anode, D12.anode, D23.anode, D24.anode, D25.anode
  N43: Teensy++1.PA2, Switch16.connector2, Switch19.connector2, Switch22.connector2, Switch25.connector2
  N44: Teensy++1.PA3, Switch14.connector2, Switch17.connector2, Switch20.connector2, Switch23.connector2, Switch26.connector2
  N45: Teensy++1.PA4, GLCD_128x1.connector14
  N46: Teensy++1.PA5, GLCD_128x1.connector5
  N47: Teensy++1.PA6, GLCD_128x1.connector4
  N48: Teensy++1.PA7, GLCD_128x1.connector3
  N49: Switch1.connector3, D1.cathode
  N50: Switch2.connector3, D2.cathode
  N51: Switch3.connector3, D3.cathode
  N52: Switch4.connector3, D4.cathode
  N53: Switch5.connector3, D5.cathode
  N54: Switch6.connector3, D6.cathode
  N55: Switch7.connector3, D7.cathode
  N56: Switch8.connector3, D8.cathode
  N57: Switch9.connector3, D9.cathode
  N58: Switch10.connector3, D10.cathode
  N59: Switch11.connector3, D11.cathode
  N60: Switch12.connector3, D12.cathode
  N61: Switch13.connector3, D13.cathode
  N62: Switch14.connector0, D16.cathode
  N63: Switch15.connector0, D15.cathode
  N64: Switch16.connector0, D14.cathode
  N65: Switch17.connector0, D18.cathode
  N66: Switch18.connector0, D17.cathode
  N67: Switch19.connector0, D19.cathode
  N68: Switch20.connector0, D22.cathode
  N69: Switch21.connector0, D20.cathode
  N70: Switch22.connector0, D21.cathode
  N71: Switch23.connector0, D23.cathode
  N72: Switch24.connector0, D24.cathode
  N73: Switch25.connector0, D25.cathode
  N74: Switch26.connector0, D26.cathode
  N75: LED1.connector0, R2.Pin_0
  N76: LED1.connector2, R1.Pin_0
  N77: LED2.connector0, R3.Pin_0
  N78: LED2.connector2, R4.Pin_0
  N79: LED3.connector0, R5.Pin_0
  N80: LED3.connector2, R6.Pin_0
  N81: LED4.connector0, R11.Pin_0
  N82: LED4.connector2, R8.Pin_0
  N83: LED5.connector0, R9.Pin_0
  N84: LED5.connector2, R13.Pin_0
  N85: LED6.connector0, R10.Pin_0
  N86: LED6.connector2, R14.Pin_0
  N87: LED7.connector0, R19.Pin_0
  N88: LED7.connector2, R12.Pin_0
  N89: LED8.connector0, R16.Pin_0
  N90: LED8.connector2, R18.Pin_0
  N91: LED9.connector0, R20.Pin_0
  N92: LED9.connector2, R17.Pin_0
  N93: S1.COM, VCC1.connector1
  N94: S1.L2, DC-DC1.connector0
  N95: Q1.E, R23.Pin_0
  N96: Q1.B, R22.Pin_1
  N97: R23.Pin_1, GLCD_128x1.connector18
  N98: GLCD_128x1.connector2, R21.wiper
  N99: GLCD_128x1.connector17, R21.leg1
  N100: R24.Pin_0, J1.pin2
