# Fritzing sketch id1707_Untitled_Sketch_0 (saved by Fritzing 0.8.7b)
circuit board: 6.88566cm x 5.36311cm
breadboards: 1

parts:
  Bauteil1 = Arduino Uno (Rev3)
  part = male pin header, 8 pins [form="♂ (male)"]
  part_2 = male pin header, 8 pins [form="♂ (male)"]

nets:
  N1: Bauteil1.A0, part_2.pin4
  N2: Bauteil1.A1, part_2.pin3
  N3: Bauteil1.A2, part_2.pin2
  N4: Bauteil1.A3, part_2.pin1
  N5: Bauteil1.D8, part.pin2
  N6: Bauteil1.D9_PWM, part.pin1
  N7: Bauteil1.D10_PWM/SS, part_2.pin5
  N8: Bauteil1.D11_PWM/MOSI, part_2.pin6
  N9: Bauteil1.D12/MISO, part_2.pin7
  N10: Bauteil1.D13/SCK, part_2.pin8
  N11: Bauteil1.D2, part.pin8
  N12: Bauteil1.D3_PWM, part.pin7
  N13: Bauteil1.D4, part.pin6
  N14: Bauteil1.D5_PWM, part.pin5
  N15: Bauteil1.D6_PWM, part.pin4
  N16: Bauteil1.D7, part.pin3

notes:
  Floppy 1
  Floppy 6
  Floppy 5
  Floppy 4
  Floppy 3
  Floppy 2
  Floppy 8
  Floppy 7
  Floppy Shield for 8 Floppy drives made by shadow3264
  Floppy Shield
  for 8 Floppy drives
  made by shadow3264
