# Fritzing sketch id1708_FFFT_0 (saved by Fritzing 0.9.2b)

parts:
  FLORA1 = Adafruit_Flora
  NEOPIXEL2 = Neopixel_Strip____White__60_m
  MIC1 = MAX4466_Electret_Microphone_Breakout_Board

nets:
  N1: FLORA1.connector1, MIC1.connector2
  N2: FLORA1.connector8, NEOPIXEL2.connector2
  N3: FLORA1.connector10, NEOPIXEL2.connector1
  N4: FLORA1.connector11, NEOPIXEL2.connector3
  N5: FLORA1.connector13, MIC1.connector1
  N6: FLORA1.connector14, MIC1.connector3
