# Fritzing sketch id1709_Flux_Capacitor_0 (saved by Fritzing 0.9.3b)
breadboards: 1

parts:
  Arduino_UNO = Arduino Uno (Rev3)
  Register_1 = 74HC595 [package="DIP16 [THT]"]
  Register_3 = 74HC595 [package="DIP16 [THT]"]
  R2/Q4 = LED - 5mm [color="White (6500K)" package="5 mm [THT]"]
  R1/Q3 = LED - 5mm [color="White (8000K)" package="5 mm [THT]"]
  R1/Q2 = LED - 5mm [color="Red (633nm)" package="5 mm [THT]"]
  R1/Q1 = LED - 5mm [color="Red (633nm)" package="5 mm [THT]"]
  R1/Q0 = LED - 5mm [color="Red (633nm)" package="5 mm [THT]"]
  R1/Q4 = LED - 5mm [color="Red (633nm)" package="5 mm [THT]"]
  R1/Q5 = LED - 5mm [color="Red (633nm)" package="5 mm [THT]"]
  R1/Q6 = LED - 5mm [color="Red (633nm)" package="5 mm [THT]"]
  R1/Q7 = LED - 5mm [color="Red (633nm)" package="5 mm [THT]"]
  R2/Q5 = LED - 5mm [color="Red (633nm)" package="5 mm [THT]"]
  R3/Q0 = LED - 5mm [color="Red (633nm)" package="5 mm [THT]"]
  R3/Q1 = LED - 5mm [color="Red (633nm)" package="5 mm [THT]"]
  R3/Q2 = LED - 5mm [color="Red (633nm)" package="5 mm [THT]"]
  R2/Q3 = LED - 5mm [color="Red (633nm)" package="5 mm [THT]"]
  R2/Q2 = LED - 5mm [color="Red (633nm)" package="5 mm [THT]"]
  R2/Q1 = LED - 5mm [color="Red (633nm)" package="5 mm [THT]"]
  R2/Q0 = LED - 5mm [color="Red (633nm)" package="5 mm [THT]"]
  R2/Q6 = LED - 5mm [color="Red (633nm)" package="5 mm [THT]"]
  R2/Q6_2 = LED - 5mm [color="Red (633nm)" package="5 mm [THT]"]
  Register_2 = 74HC595 [package="DIP16 [THT]"]

nets:
  N1: Arduino_UNO.D8, Register_1.DS
  N2: Arduino_UNO.D9_PWM, Register_1.ST_CP
  N3: Arduino_UNO.D10_PWM/SS, Register_3.SH_CP
  N4: Register_1.Q1, R1/Q1.anode
  N5: Register_1.Q2, R1/Q2.anode
  N6: Register_1.Q3, R1/Q3.anode
  N7: Register_1.Q4, R1/Q4.anode
  N8: Register_1.Q5, R1/Q5.anode
  N9: Register_1.Q6, R1/Q6.anode
  N10: Register_1.Q7, R1/Q7.anode
  N11: Register_1.Q0, R1/Q0.anode
  N12: Register_3.Q1, R3/Q1.anode
  N13: Register_3.Q2, R3/Q2.anode
  N14: Register_3.VCC, R3/Q0.anode
  N15: R2/Q4.anode, Register_2.Q4
  N16: R2/Q5.anode, Register_2.Q5
  N17: R2/Q3.anode, Register_2.Q3
  N18: R2/Q2.anode, Register_2.Q2
  N19: R2/Q1.anode, Register_2.Q1
  N20: R2/Q0.anode, Register_2.Q0
  N21: R2/Q6.anode, Register_2.Q6
  N22: R2/Q6_2.anode, Register_2.Q7
