# Fritzing sketch id170_7seg_example_non_working_0 (saved by Fritzing 0.9.3b)
breadboards: 2

parts:
  S1 = Pushbutton [package=THT]
  S2 = Pushbutton [package=THT]
  S3 = Pushbutton [package=THT]
  S4 = Pushbutton [package=THT]
  R1 = Resistor [tolerance=±5% resistance=220 package=THT]
  R2 = Resistor [tolerance=±5% resistance=220 package=THT]
  R3 = Resistor [tolerance=±5% resistance=220 package=THT]
  R4 = Resistor [tolerance=±5% resistance=220 package=THT]
  V2 = DC Power [voltage=5]
  C1 = Electrolytic Capacitor [capacitance=10µF package="100 mil [THT, electrolytic]"]
  C2 = Ceramic Capacitor [capacitance=100nF package="100 mil [THT, multilayer]"]
  7_Segment1 = 7 Segment Display
  R5 = Resistor [tolerance=±5% resistance=220 package=THT]
  R6 = Resistor [tolerance=±5% resistance=220 package=THT]
  R7 = Resistor [tolerance=±5% resistance=220 package=THT]
  R8 = Resistor [tolerance=±5% resistance=220 package=THT]
  R9 = Resistor [tolerance=±5% resistance=220 package=THT]
  R10 = Resistor [tolerance=±5% resistance=220 package=THT]
  R11 = Resistor [tolerance=±5% resistance=220 package=THT]
  IC1 = IC, DIP package, 14 pins [chip_label=7404]
  IC2 = IC, DIP package, 14 pins [chip_label=7432]
  IC3 = IC, DIP package, 14 pins [chip_label=7408]
  C3 = Electrolytic Capacitor [capacitance=10µF package="100 mil [THT, electrolytic]"]
  C4 = Electrolytic Capacitor [capacitance=10µF package="100 mil [THT, electrolytic]"]
  C5 = Electrolytic Capacitor [capacitance=10µF package="100 mil [THT, electrolytic]"]
  C6 = Ceramic Capacitor [capacitance=100nF package="100 mil [THT, multilayer]"]
  C7 = Ceramic Capacitor [capacitance=100nF package="100 mil [THT, multilayer]"]
  C8 = Ceramic Capacitor [capacitance=100nF package="100 mil [THT, multilayer]"]

nets:
  GND: S1.leg0, S2.leg0, S3.leg0, S4.leg0, V2.V-, C1.-, C2.0, 7_Segment1.common_cathode, IC1.pin7, IC2.pin7, IC3.pin7, C3.-, C4.-, C5.-, C6.0, C7.0, C8.0
  Pnot: S1.leg1, R1.Pin_0, IC1.pin5
  Qnot: S2.leg1, R2.Pin_0, IC1.pin3, IC3.pin1
  Rnot: S3.leg1, R3.Pin_0, IC1.pin1
  Snot: S4.leg1, R4.Pin_0, IC1.pin9, IC3.pin2
  5V/Vcc: R1.Pin_1, R2.Pin_1, R3.Pin_1, R4.Pin_1, V2.V+, C1.+, C2.1, IC1.pin14, IC2.pin14, IC3.pin14, C3.+, C4.+, C5.+, C6.1, C7.1, C8.1
  N1: 7_Segment1.Segment_A#1, R11.Pin_1
  N2: 7_Segment1.Segment_F, R10.Pin_1
  N3: 7_Segment1.Segment_E, R9.Pin_1
  N4: 7_Segment1.Segment_D, R8.Pin_1
  N5: 7_Segment1.Segment_C, R7.Pin_1
  N6: 7_Segment1.Segment_B, R6.Pin_1
  N7: 7_Segment1.Segment_A#10, R5.Pin_1
  a: R5.Pin_0, IC2.pin3
  b: R6.Pin_0
  c: R7.Pin_0
  d: R8.Pin_0
  e: R9.Pin_0
  f: R10.Pin_0
  g: R11.Pin_0
  N8: IC1.pin4, IC3.pin4
  N9: IC1.pin8, IC3.pin5
  N10: IC2.pin1, IC3.pin3
  N11: IC2.pin2, IC3.pin6

notes:
  CETT1425 7 Segment Decoder, 4 bit Hexadecimal Seven Segment Decoder
  NC, no need to connect the decimal point
  Snot
  Pnot
  Rnot
  Qnot
