# Fritzing sketch id1710_interruptRC_0 (saved by Fritzing 0.9.3b)
circuit board: 5cm x 3cm
breadboards: 1

parts:
  Componente2 = adafruit [part_number=2011]
  J2 = male alternating pin header, 3 pins [form="♂ (male)"]
  J3 = male alternating pin header, 3 pins [form="♂ (male)"]  # not connected
  J4 = male alternating pin header, 3 pins [form="♂ (male)"]  # not connected
  J5 = male alternating pin header, 3 pins [form="♂ (male)"]
  J6 = male alternating pin header, 3 pins [form="♂ (male)"]
  J7 = male alternating pin header, 3 pins [form="♂ (male)"]
  J8 = male alternating pin header, 3 pins [form="♂ (male)"]
  Componente3 = Arduino Mega 2560 (Rev3)
  J9 = Basic Servo
  J10 = Basic Servo
  J12 = Basic Servo
  J11 = Basic Servo

nets (from the breadboard view):
  GND: Componente2.connector1, J2.pin1, Componente3.GND, J9.gnd, J10.gnd, J12.gnd, J11.gnd
  VCC: Componente2.connector2, J2.pin2, J9.vcc, J10.vcc, J12.vcc, J11.vcc
  N1: J5.pin3, Componente3.D3_PWM
  N2: J6.pin3, Componente3.D18/TX1
  N3: J7.pin3, Componente3.D2_PWM
  N4: J8.pin3, Componente3.D19/RX1
  N5: Componente3.D10_PWM, J10.pulse
  N6: Componente3.D9_PWM, J12.pulse
