# Fritzing sketch id1711_SHT71_Flyport_0 (saved by Fritzing 0.4.3b)

parts:
  R1_10K = Resistor [resistance=10k package=THT]
  SHT71 = StarterKit Nest
  Componente3 = SHT71

nets:
  N1: R1_10K.Pin_0, SHT71.connector1pin-5, Componente3.connector3
  N2: R1_10K.Pin_1, SHT71.connector2pin-2-6-3, Componente3.connector1
  N3: SHT71.connector0pin-1, Componente3.connector0
  N4: SHT71.connector0pin-6-9-1, Componente3.connector2
