# Fritzing sketch id1712_FM_Transmitter_0 (saved by Fritzing 0.9.3b)
circuit board: 8.46667cm x 5.64444cm
breadboards: 1

parts:
  R1 = Resistor [tolerance=±5% resistance=22k package=THT]
  R2 = Resistor [tolerance=±5% resistance=10k package=THT]
  R3 = Resistor [tolerance=±5% resistance=47k package=THT]
  R4 = Resistor [tolerance=±5% resistance=1M package=THT]
  R5 = Resistor [tolerance=±5% resistance=470 package=THT]
  C1 = Ceramic Capacitor [capacitance=27pF package="100 mil [THT, multilayer]"]
  C2 = Ceramic Capacitor [capacitance=100nF package="100 mil [THT, multilayer]"]
  C3 = Ceramic Capacitor [capacitance=2.2µF package="100 mil [THT, multilayer]"]
  C4 = Ceramic Capacitor [capacitance=1mF package="100 mil [THT, multilayer]"]
  C5 = Ceramic Capacitor [capacitance=5.6pF package="100 mil [THT, multilayer]"]
  C6 = Ceramic Capacitor [capacitance=10nF package="100 mil [THT, multilayer]"]
  Q1 = NPN-Transistor [package="TO92 [THT]"]
  Q2 = NPN-Transistor [package="TO92 [THT]"]
  Part1 = Variable Capacitor [capacitance=100nF max_capacitance=45pF min_capacitance=6pF voltage=35V]
  ANT1 = Antenna
  MIC1 = Microphone
  VCC1 = Battery block 9V

nets:
  N1: R1.Pin_0, C3.0, MIC1.pin2
  N2: R1.Pin_1, R2.Pin_1, R3.Pin_1, Part1.1
  N3: R2.Pin_0, R4.Pin_1, C2.0, Q1.C
  N4: R3.Pin_0, C2.1, C4.1, Q2.B
  N5: R4.Pin_0, C3.1, Q1.B
  N6: R5.Pin_0, C4.0, C6.0, Q1.E, MIC1.pin1, VCC1.-
  N7: R5.Pin_1, C5.0, Q2.E
  N8: C1.0, C5.1, Q2.C, Part1.0
  N9: C1.1, ANT1.antenna_lead
  N10: C6.1, Part1.2, VCC1.+
