# Fritzing sketch id1713_RAW_Fritzing_PCB_File_0 (saved by Fritzing 0.8.3b)
circuit board: 3.2cm x 1.4cm
breadboards: 1

parts:
  part = mystery part, 2 pins [chip_label=?]
  part_2 = Resistor [tolerance=±5% resistance=220 package=THT]
  part_3 = Ceramic Capacitor [capacitance=100nF package="200 mil [THT, multilayer]"]
  part_4 = Resistor [tolerance=±5% resistance=220 package=THT]
  part_5 = Resistor [tolerance=±5% resistance=220 package=THT]
  part_6 = NPN-Transistor [package="TO92 [THT]"]
  part_7 = Resistor [tolerance=±5% resistance=220 package=THT]
  part_8 = Resistor [tolerance=±5% resistance=220 package=THT]
  part_9 = Ceramic Capacitor [capacitance=100nF package="200 mil [THT, multilayer]"]
  part_10 = Resistor [tolerance=±5% resistance=220 package=THT]
  part_11 = Ceramic Capacitor [capacitance=100nF package="100 mil [THT, multilayer]"]
  part_12 = NPN-Transistor [package="TO92 [THT]"]
  part_13 = Resistor [tolerance=±5% resistance=220 package=THT]
  part_14 = mystery part, 1 pin [chip_label=?]
  part_15 = mystery part, 1 pin [chip_label=?]
  part_16 = mystery part, 1 pin [chip_label=?]
  part_17 = mystery part, 1 pin [chip_label=?]
  part_18 = Ceramic Capacitor [capacitance=100nF package="200 mil [THT, multilayer]"]
  part_19 = mystery part, 1 pin [chip_label=?]
  part_20 = mystery part, 1 pin [chip_label=?]
  part_21 = mystery part, 1 pin [chip_label=?]

nets:
  N1: part.pin1, part_2.Pin_1, part_3.1
  N2: part.pin2, part_5.Pin_1, part_7.Pin_0, part_10.Pin_0, part_19.pin1
  N3: part_2.Pin_0, part_4.Pin_1, part_8.Pin_0, part_11.0, part_13.Pin_1, part_14.pin1, part_17.pin1, part_20.pin1
  N4: part_3.0, part_4.Pin_0, part_5.Pin_0, part_6.B
  N5: part_6.E, part_7.Pin_1
  N6: part_6.C, part_8.Pin_1, part_9.0
  N7: part_9.1, part_11.1, part_12.B, part_13.Pin_0
  N8: part_10.Pin_1, part_12.E, part_18.1
  N9: part_12.C, part_15.pin1, part_16.pin1, part_18.0, part_21.pin1
