# Fritzing sketch id1714_secuencia_6_leds_marco_0 (saved by Fritzing 0.7.5b)
breadboards: 1

parts:
  R1 = Resistor [tolerance=±5% resistance=220 package=THT]
  LED1 = LED - 5mm [color="Red (633nm)" package="5 mm [THT]"]
  R2 = Resistor [tolerance=±5% resistance=220 package=THT]
  R3 = Resistor [tolerance=±5% resistance=220 package=THT]
  LED4 = LED - 5mm [color="Red (633nm)" package="5 mm [THT]"]
  R4 = Resistor [tolerance=±5% resistance=220 package=THT]
  LED5 = smd LED [color="Yellow (585nm)" package="1206 [SMD]"]
  LED11 = smd LED [color="Green (555nm)" package="1206 [SMD]"]
  R5 = Resistor [tolerance=±5% resistance=220 package=THT]
  R6 = Resistor [tolerance=±5% resistance=220 package=THT]
  LED12 = smd LED [color="Yellow (585nm)" package="1206 [SMD]"]
  LED13 = smd LED [color="Green (555nm)" package="1206 [SMD]"]
  Arduino1 = Arduino  # not connected

nets:
  N1: R1.Pin_0, LED1.cathode
  N2: R1.Pin_1, R2.Pin_1, R3.Pin_1, R4.Pin_1, R5.Pin_1, R6.Pin_1
  N3: R2.Pin_0, LED5.cathode
  N4: R3.Pin_0, LED11.cathode
  N5: LED4.cathode, R4.Pin_0
  N6: R5.Pin_0, LED12.cathode
  N7: R6.Pin_0, LED13.cathode
