# Fritzing sketch id1718_I2C_to_1_WIRE_0 (saved by Fritzing 0.7.10b)
breadboards: 1

parts:
  DS2483 = SO08 [chip_label=DS2482 package=SO]
  R3 = Resistor [tolerance=±5% resistance=2.2k package="0805 [SMD]"]
  R4 = Resistor [tolerance=±5% resistance=2.2k package="0805 [SMD]"]
  I2C1 = female pin header, 2 pins [form="♀ (female)"]
  PWR1 = female pin header, 2 pins [form="♀ (female)"]
  1-WIRE1 = female pin header, 2 pins [form="♀ (female)"]

nets:
  N1: DS2483.1, DS2483.7, R3.Pin_0, R4.Pin_0, PWR1.pin2
  N2: DS2483.2, 1-WIRE1.pin1
  N3: DS2483.3, DS2483.8, PWR1.pin1, 1-WIRE1.pin2
  N4: DS2483.4, R3.Pin_1, I2C1.pin1
  N5: DS2483.5, R4.Pin_1, I2C1.pin2

notes:
  DC2ZP
