# Fritzing sketch id171_example_7segments_anode_cathode_0 (saved by Fritzing 0.9.1b)
breadboards: 1

parts:
  7_Segment1 = 7 Segment Display
  7_Segment2 = 7 Segment Display
  Part1 = Arduino Mega ADK (Rev3)
  J1 = Piezo Speaker

nets:
  N1: 7_Segment1.Segment_E, Part1.D11_PWM
  N2: 7_Segment1.Segment_D, Part1.D10_PWM
  N3: 7_Segment1.common_anode, Part1.5V
  N4: 7_Segment1.Segment_C, Part1.D9_PWM
  N5: 7_Segment1.Segment_DP, Part1.D8_PWM
  N6: 7_Segment1.Segment_B, Part1.D4_PWM
  N7: 7_Segment1.Segment_A, Part1.D5_PWM
  N8: 7_Segment1.Segment_F, Part1.D6_PWM
  N9: 7_Segment1.Segment_G, Part1.D7_PWM
  N10: 7_Segment2.Segment_E, Part1.D34
  N11: 7_Segment2.Segment_D, Part1.D35
  N12: 7_Segment2.common_cathode, Part1.GND, J1.pin1
  N13: 7_Segment2.Segment_C, Part1.D36
  N14: 7_Segment2.Segment_DP, Part1.D37
  N15: 7_Segment2.Segment_B, Part1.D33
  N16: 7_Segment2.Segment_A, Part1.D32
  N17: 7_Segment2.Segment_F, Part1.D31
  N18: 7_Segment2.Segment_G, Part1.D30
  N19: Part1.D42, J1.pin2
