# Fritzing sketch id1722_Untitled_Sketch_0 (saved by Fritzing 0.9.3b)
breadboards: 1

parts:
  Raspberry_Pi_1 = Raspberry Pi 3 [part_number=RPI-3-V1.2]
  C1 = Electrolytic Capacitor [capacitance=1µF package="100 mil [THT, electrolytic]"]
  S1 = Pushbutton [package="[THT]"]
  S2 = Pushbutton [package="[THT]"]
  R1 = Resistor [tolerance=±5% resistance=220 package=THT]
  R2 = Resistor [tolerance=±5% resistance=220 package=THT]
  D1 = Rectifier Diode [part_number=1N4001 package="300 mil [THT]"]
  R3 = Resistor [tolerance=±5% resistance=220 package=THT]
  Q1 = NPN-Transistor [package="TO92 [THT]"]
  M1 = DC Motor

nets:
  N1: Raspberry_Pi_1.3v3, C1.+, R1.Pin_0, R2.Pin_0, D1.cathode, M1.pin_1
  N2: Raspberry_Pi_1.GND, C1.-, S1.Pin_3, S1.Pin_4, S2.Pin_3, S2.Pin_4, Q1.E
  N3: Raspberry_Pi_1.GIPO19, S2.Pin_1, S2.Pin_2, R2.Pin_1
  N4: Raspberry_Pi_1.GIPO26, S1.Pin_1, S1.Pin_2, R1.Pin_1
  N5: D1.anode, Q1.C, M1.pin_2
  N6: R3.Pin_1, Q1.B
