# Fritzing sketch id1723_20170804_Force_presure_sensor_0 (saved by Fritzing 0.9.3b)
breadboards: 1

parts:
  Part1 = Arduino Uno (Rev3)
  J1 = Basic Force Sensing Resistor (FSR) [package=THT]
  R1 = Resistor [tolerance=±5% resistance=220 package=THT]

nets:
  N1: Part1.A0, R1.Pin_0
  N2: Part1.5V, J1.pin_1
  N3: J1.pin_0, R1.Pin_1
