# Fritzing sketch id1725_Photores7x4_0 (saved by Fritzing 0.9.3b)
breadboards: 2

parts:
  R1 = Resistor [tolerance=±5% resistance=220 package=THT]
  R2 = Resistor [tolerance=±5% resistance=220 package=THT]
  R3 = Resistor [tolerance=±5% resistance=220 package=THT]
  R4 = Resistor [tolerance=±5% resistance=220 package=THT]  # not connected
  7_Segment_4_Digit_Display1 = MyPart1 [part_number=HS420561K-32]
  Part1 = Arduino Uno (Rev3)
  R5 = PHOTOCELL [package=photocell]
  R6 = Resistor [tolerance=±5% resistance=330 package=THT]
  R7 = PHOTOCELL [package=photocell]  # not connected
  R8 = Resistor [tolerance=±5% resistance=330 package=THT]  # not connected
  Part2 = Arduino Uno (Rev3)  # not connected
  R9 = Resistor [tolerance=±5% resistance=220 package=THT]  # not connected
  R10 = Resistor [tolerance=±5% resistance=220 package=THT]  # not connected
  R11 = Resistor [tolerance=±5% resistance=220 package=THT]  # not connected
  R12 = Resistor [tolerance=±5% resistance=220 package=THT]  # not connected

nets:
  N1: R1.Pin_0, Part1.D5_PWM
  N2: R1.Pin_1, 7_Segment_4_Digit_Display1.connector6
  N3: R2.Pin_0, Part1.D4
  N4: R2.Pin_1, 7_Segment_4_Digit_Display1.connector8, 7_Segment_4_Digit_Display1.connector9
  N5: R3.Pin_0, Part1.D3_PWM
  N6: R3.Pin_1, 7_Segment_4_Digit_Display1.connector12
  N7: 7_Segment_4_Digit_Display1.connector1, Part1.D10_PWM/SS
  N8: 7_Segment_4_Digit_Display1.connector2, Part1.D9_PWM
  N9: 7_Segment_4_Digit_Display1.connector3, Part1.D13/SCK
  N10: 7_Segment_4_Digit_Display1.connector4, Part1.D8
  N11: 7_Segment_4_Digit_Display1.connector5, Part1.D12/MISO
  N12: 7_Segment_4_Digit_Display1.connector7, Part1.D7
  N13: 7_Segment_4_Digit_Display1.connector10, Part1.D11_PWM/MOSI
  N14: 7_Segment_4_Digit_Display1.connector11, Part1.D6_PWM
  N15: Part1.A0, R5.P$1, R6.Pin_1
  N16: Part1.5V, R5.P$2
  N17: Part1.GND, R6.Pin_0

notes:
  Materiale necessario:
  1 Arduino.
  1 Breadboard.
  1 Display 4 digit, 7 segmenti.
  1 Resistenza 330ohm.
  4 Resistenze 220 ohm.
  Cavi connettori.
