# Fritzing sketch id1726_Fotosensor_0 (saved by Fritzing 0.9.3b)
breadboards: 1

parts:
  Parça1 = Arduino Uno (Rev3)
  R1 = Photocell (LDR) [package=THT]
  R2 = Resistor [tolerance=±5% resistance=10k package=THT]
  LED1 = LED - 5mm [color="Red (633nm)" package="5 mm [THT]"]
  R3 = Resistor [tolerance=±20% resistance=220 package=THT]

nets:
  N1: Parça1.A0, R1.pin_0, R2.Pin_1
  N2: Parça1.D9_PWM, LED1.anode
  N3: Parça1.5V, R2.Pin_0
  N4: Parça1.GND, R1.pin_1, R3.Pin_0
  N5: LED1.cathode, R3.Pin_1
