# Fritzing sketch id1727_Buttons_0 (saved by Fritzing 0.9.3b)
breadboards: 1

parts:
  Onderdeel1 = Arduino Uno (Rev3)
  S1 = Pushbutton [package="[THT]"]
  S2 = Pushbutton [package="[THT]"]
  R1 = Resistor [tolerance=±5% resistance=1k package="2010 [SMD]"]
  R2 = Resistor [tolerance=±5% resistance=10k package="2010 [SMD]"]
  R3 = Resistor [tolerance=±5% resistance=1k package="2010 [SMD]"]
  R4 = Resistor [tolerance=±5% resistance=10k package="2010 [SMD]"]
  S3 = Pushbutton [package="[THT]"]
  S4 = Pushbutton [package="[THT]"]
  R5 = Resistor [tolerance=±5% resistance=10k package="2010 [SMD]"]
  R6 = Resistor [tolerance=±5% resistance=10k package="2010 [SMD]"]
  R7 = Resistor [tolerance=±5% resistance=1k package="2010 [SMD]"]
  R8 = Resistor [tolerance=±5% resistance=1k package="2010 [SMD]"]
  LED1 = LED - 5mm [color="Green (555nm)" package="5 mm [THT]"]
  R9 = Resistor [tolerance=±5% resistance=220 package=THT]
  LED2 = LED - 5mm [color="Red (633nm)" package="5 mm [THT]"]
  R10 = Resistor [tolerance=±5% resistance=220 package=THT]

nets:
  N1: Onderdeel1.D8, S1.Pin_1, S1.Pin_2, R4.Pin_1
  N2: Onderdeel1.D9_PWM, S2.Pin_1, S2.Pin_2, R2.Pin_1
  N3: Onderdeel1.D10_PWM/SS, S3.Pin_1, S3.Pin_2, R5.Pin_1
  N4: Onderdeel1.D11_PWM/MOSI, S4.Pin_1, S4.Pin_2, R6.Pin_1
  N5: Onderdeel1.D2, LED1.anode
  N6: Onderdeel1.D5_PWM, LED2.anode
  N7: Onderdeel1.5V, R1.Pin_0, R3.Pin_0, R7.Pin_0, R8.Pin_0
  N8: Onderdeel1.GND, R2.Pin_0, R4.Pin_0, R5.Pin_0, R6.Pin_0, R9.Pin_0, R10.Pin_0
  N9: S1.Pin_3, S1.Pin_4, R3.Pin_1
  N10: S2.Pin_3, S2.Pin_4, R1.Pin_1
  N11: S3.Pin_3, S3.Pin_4, R7.Pin_1
  N12: S4.Pin_3, S4.Pin_4, R8.Pin_1
  N13: LED1.cathode, R9.Pin_1
  N14: LED2.cathode, R10.Pin_1
