# Fritzing sketch id1728_buoy_2.3_fritzing_0 (saved by Fritzing 0.9.1b)
breadboards: 1

parts:
  Part1 = Arduino Uno (Rev3)
  R1 = Resistor [tolerance=±5% resistance=100 package=THT]
  R2 = Resistor [tolerance=±5% resistance=100 package=THT]
  LED1 = LED - 5mm [color="Orange (612nm)" package="5 mm [THT]"]
  LED2 = LED - 5mm [color="Green (565nm)" package="5 mm [THT]"]
  R3 = Resistor [tolerance=±5% resistance=100 package=THT]
  LED3 = LED - 5mm [color="Red (633nm)" package="5 mm [THT]"]
  R4 = Resistor [tolerance=±5% resistance=100 package=THT]
  LED4 = LED - 5mm [color="Blue (470nm)" package="5 mm [THT]"]
  IC1 = IC, DIP package, 6 pins [chip_label=28036]

nets:
  N1: Part1.D10_PWM/SS, R2.Pin_0
  N2: Part1.D11_PWM/MOSI, R3.Pin_0
  N3: Part1.D12/MISO, R4.Pin_0
  N4: Part1.D13/SCK, R1.Pin_0
  N5: Part1.D6_PWM, IC1.pin3
  N6: Part1.D7, IC1.pin4
  N7: Part1.5V, IC1.pin5
  N8: Part1.GND, LED1.anode, LED2.anode, LED3.anode, LED4.anode, IC1.pin6
  N9: R1.Pin_1, LED2.cathode
  N10: R2.Pin_1, LED1.cathode
  N11: R3.Pin_1, LED3.cathode
  N12: R4.Pin_1, LED4.cathode
