# Fritzing sketch id1729_Schematic_0 (saved by Fritzing 0.9.3b)
breadboards: 1

parts:
  Raspberry_Pi_1 = Raspberry Pi 3 [part_number=RPI-3-V1.2]
  Cmod_A1 = CmodA7
  R2 = Resistor [tolerance=±5% resistance=220 package=THT]
  S1 = Pushbutton [package=THT]
  R3 = Resistor [tolerance=±5% resistance=220 package=THT]
  LED1 = LED - 5mm [color="Red (633nm)" package="5 mm [THT]"]

nets:
  N1: Raspberry_Pi_1.GPIO10, Cmod_A1.connector1
  N2: Raspberry_Pi_1.GPIO9, Cmod_A1.connector0
  N3: Raspberry_Pi_1.GPIO11, Cmod_A1.connector2
  N4: Raspberry_Pi_1.GPIO25, Cmod_A1.connector3
  N5: Raspberry_Pi_1.GND, Cmod_A1.connector58
  N6: R2.Pin_0, S1.leg0
  N7: S1.leg1, R3.Pin_0
  N8: R3.Pin_1, LED1.anode
