# Fritzing sketch id172_7_segment_0 (saved by Fritzing 0.9.3b)
breadboards: 1

parts:
  R1 = Resistor [tolerance=±5% resistance=220 package=THT]
  7_Segment1 = 7 Segment Display
  Bauteil1 = Arduino Uno (Rev3) - ICSP
  R2 = Resistor [tolerance=±5% resistance=220 package=THT]

nets:
  N1: R1.Pin_0, 7_Segment1.common_cathode, R2.Pin_0
  N2: R1.Pin_1, Bauteil1.GND, R2.Pin_1
  N3: 7_Segment1.Segment_E, Bauteil1.D6_PWM
  N4: 7_Segment1.Segment_D, Bauteil1.D5_PWM
  N5: 7_Segment1.Segment_C, Bauteil1.D4
  N6: 7_Segment1.Segment_B, Bauteil1.D3_PWM
  N7: 7_Segment1.Segment_A, Bauteil1.D2
  N8: 7_Segment1.Segment_F, Bauteil1.D8
  N9: 7_Segment1.Segment_G, Bauteil1.D9_PWM
