# Fritzing sketch id1736_Emergency_Flasher (saved by Fritzing 0.6.2b)
breadboards: 1

parts:
  Arduino1 = Arduino Mega
  LED1 = Red LED - 5mm [package="5 mm [THT]"]
  LED2 = Red LED - 5mm [package="5 mm [THT]"]
  LED3 = Red LED - 5mm [package="5 mm [THT]"]
  LED4 = Red LED - 5mm [package="5 mm [THT]"]
  LED5 = Red LED - 5mm [package="5 mm [THT]"]
  LED6 = Red LED - 5mm [package="5 mm [THT]"]
  LED12 = Blue LED - 5mm [package="5 mm [THT]"]
  LED10 = Blue LED - 5mm [package="5 mm [THT]"]
  LED8 = Blue LED - 5mm [package="5 mm [THT]"]
  LED9 = Blue LED - 5mm [package="5 mm [THT]"]
  LED11 = Blue LED - 5mm [package="5 mm [THT]"]
  LED7 = Blue LED - 5mm [package="5 mm [THT]"]

nets:
  N1: Arduino1.D12, LED1.anode, LED2.anode, LED3.anode, LED4.anode, LED5.anode, LED6.anode
  N2: Arduino1.D10, LED12.anode, LED10.anode, LED8.anode, LED9.anode, LED11.anode, LED7.anode
  N3: Arduino1.GND, LED1.cathode, LED2.cathode, LED3.cathode, LED4.cathode, LED5.cathode, LED6.cathode, LED12.cathode, LED10.cathode, LED8.cathode, LED9.cathode, LED11.cathode, LED7.cathode
