# Fritzing sketch id173_Untitled_Sketch_0 (saved by Fritzing 0.9.0b)
breadboards: 1

parts:
  7_Segment1 = 7 Segment Display
  Part1 = Arduino Leonardo (Rev3b)
  IR1 = TSOP312.., 314.. [package=THT]
  R2 = Resistor [tolerance=±5% resistance=330 package=THT]
  R1 = Resistor [tolerance=±5% resistance=220 package=THT]

nets:
  N1: 7_Segment1.Segment_E, Part1.D5_PWM
  N2: 7_Segment1.Segment_D, Part1.D6_PWM/A7
  N3: 7_Segment1.common_anode, R2.Pin_0, R1.Pin_1
  N4: 7_Segment1.Segment_C, Part1.D7
  N5: 7_Segment1.Segment_B, Part1.A0
  N6: 7_Segment1.Segment_A, Part1.D2/SDA
  N7: 7_Segment1.Segment_F, Part1.D3_PWM/SCL
  N8: 7_Segment1.Segment_G, Part1.D4/A6
  N9: Part1.5V, IR1.Data
  GND: Part1.GND, IR1.GND, R2.Pin_1, R1.Pin_0
  N10: Part1.D11_PWM, IR1.Vs
