# Fritzing sketch id174_seven_segment_led_clock_0 (saved by Fritzing 0.9.2b)
breadboards: 1

parts:
  Shift_Register = 74HC595 [package="DIP16 [THT]"]
  Arduino = Arduino Uno (Rev3)
  RTC = Real Time Clock Module - DS1307 RTC Breakout Board
  R1 = Resistor [tolerance=±5% resistance=220 package=THT]
  R2 = Resistor [tolerance=±5% resistance=220 package=THT]
  R3 = Resistor [tolerance=±5% resistance=220 package=THT]
  R4 = Resistor [tolerance=±5% resistance=220 package=THT]
  R5 = Resistor [tolerance=±5% resistance=220 package=THT]
  R6 = Resistor [tolerance=±5% resistance=220 package=THT]
  R7 = Resistor [tolerance=±5% resistance=220 package=THT]
  R8 = Resistor [tolerance=±5% resistance=220 package=THT]
  Date_Button = Pushbutton [package="[THT]"]
  7_Segment_H1 = 7 Segment Display
  7_Segment_H2 = 7 Segment Display
  7_Segment_M1 = 7 Segment Display
  7_Segment_M2 = 7 Segment Display

nets:
  N1: Shift_Register.Q1, R1.Pin_0
  N2: Shift_Register.Q2, R2.Pin_0
  N3: Shift_Register.Q3, R3.Pin_0
  N4: Shift_Register.Q4, R4.Pin_0
  N5: Shift_Register.Q5, R5.Pin_0
  N6: Shift_Register.Q6, R6.Pin_0
  N7: Shift_Register.Q7, R7.Pin_0
  GND: Shift_Register.GND, Shift_Register.OE, Arduino.GND, RTC.GND, Date_Button.Pin_3, Date_Button.Pin_4
  5V: Shift_Register.MR, Shift_Register.VCC, Arduino.5V, RTC.5V
  N8: Shift_Register.SH_CP, Arduino.D11_PWM/MOSI
  N9: Shift_Register.ST_CP, Arduino.D12/MISO
  N10: Shift_Register.DS, Arduino.D13/SCK
  N11: Arduino.A4/SDA, RTC.SDA
  N12: Arduino.A5/SCL, RTC.SCL
  N13: Arduino.D9_PWM, Date_Button.Pin_1, Date_Button.Pin_2
  N14: Arduino.D1/TX, 7_Segment_H1.common_anode
  N15: Arduino.D2, 7_Segment_H2.common_anode
  N16: Arduino.D3_PWM, 7_Segment_M1.common_anode
  N17: Arduino.D4, 7_Segment_M2.common_anode
  N18: Arduino.D7, R8.Pin_1
  N19: R1.Pin_1, 7_Segment_H1.Segment_E, 7_Segment_H2.Segment_E, 7_Segment_M1.Segment_E, 7_Segment_M2.Segment_E
  N20: R2.Pin_1, 7_Segment_H1.Segment_D, 7_Segment_H2.Segment_D, 7_Segment_M1.Segment_D, 7_Segment_M2.Segment_D
  N21: R3.Pin_1, 7_Segment_H1.Segment_C, 7_Segment_H2.Segment_C, 7_Segment_M1.Segment_C, 7_Segment_M2.Segment_C
  N22: R4.Pin_1, 7_Segment_H1.Segment_B, 7_Segment_H2.Segment_B, 7_Segment_M1.Segment_B, 7_Segment_M2.Segment_B
  N23: R5.Pin_1, 7_Segment_H1.Segment_A, 7_Segment_H2.Segment_A, 7_Segment_M1.Segment_A, 7_Segment_M2.Segment_A
  N24: R6.Pin_1, 7_Segment_H1.Segment_F, 7_Segment_H2.Segment_F, 7_Segment_M1.Segment_F, 7_Segment_M2.Segment_F
  N25: R7.Pin_1, 7_Segment_H1.Segment_G, 7_Segment_H2.Segment_G, 7_Segment_M1.Segment_G, 7_Segment_M2.Segment_G
  N26: R8.Pin_0, 7_Segment_H2.Segment_DP

notes:
  Display Date Button
