# Fritzing sketch id1755_Pulsewidth_Modulator_0 (saved by Fritzing 0.9.2b)
circuit board: 4.69573cm x 3.43912cm
breadboards: 1

parts:
  R1 = Resistor [tolerance=±5% resistance=220 package=THT]
  D1 = Rectifier Diode [part_number=1N4148 package="300 mil [THT]"]
  IC1 = General purpose bipolar Timer [package=dil-08]
  D2 = Rectifier Diode [part_number=1N4148 package="300 mil [THT]"]
  R2 = Resistor [tolerance=±5% resistance=220 package=THT]
  C3 = Tantalum Capacitor [capacitance=1µF package="200 mil [THT, tantalum]"]
  P2_Freq = Trimmer Potentiometer [maximum_resistance=100kΩ package=THT]
  BAT1 = BC9VPC [package=bc9vpc]
  P1_Pulse = Trimmer Potentiometer [maximum_resistance=1MΩ package=THT]
  C1 = Electrolytic Capacitor [capacitance=22nF package="200 mil [THT, electrolytic]"]

nets:
  N1: R1.Pin_0, D1.anode, IC1.DIS, R2.Pin_0
  N2: R1.Pin_1, IC1._RES, IC1.VCC+, BAT1.V+
  N3: D1.cathode, P2_Freq.leg2
  N4: IC1.GND, C3.-, BAT1.V-, C1.-
  N5: IC1.TRI, IC1.TRE, P1_Pulse.leg1, P1_Pulse.wiper, C1.+
  N6: IC1.CON, C3.+
  N7: D2.cathode, R2.Pin_1
  N8: D2.anode, P2_Freq.leg1
  N9: P2_Freq.wiper, P1_Pulse.leg2
