# Fritzing sketch id1756_Platine_Frequenzerzeugung_0 (saved by Fritzing 0.9.0b)
circuit board: 8.46667cm x 5.64444cm
breadboards: 1

parts:
  U1 = 555 Timer [package="DIP8 [THT]"]
  V1 = DC Power [voltage=12V]
  C1 = Ceramic Capacitor [capacitance=4.7µF package="100 mil [THT, multilayer]"]
  C3 = Ceramic Capacitor [capacitance=1µF package="100 mil [THT, multilayer]"]
  C2 = Ceramic Capacitor [capacitance=1µF package="100 mil [THT, multilayer]"]
  R1 = Resistor [tolerance=±5% resistance=330 package=THT]
  R2 = Resistor [tolerance=±5% resistance=220 package=THT]
  R3 = Resistor [tolerance=±5% resistance=220 package=THT]
  R4 = Trimmer Potentiometer [maximum_resistance=0.1MΩ package=THT]

nets:
  N1: U1.Ground, V1.V+, C2.0, R1.Pin_0, R3.Pin_1
  N2: U1.Trigger, C1.1
  N3: U1.Output, C1.0
  N4: U1.Reset, R4.leg1
  N5: U1.Control_Voltage, C3.1, R2.Pin_0, R3.Pin_0
  N6: U1.Threshold, V1.V-, C3.0, C2.1, R2.Pin_1, R4.wiper
  N7: U1.Discharge, R1.Pin_1
