# Fritzing sketch id1757_Untitled_Sketch20_0 (saved by Fritzing 0.9.2b)
breadboards: 1

parts:
  R1 = Resistor [tolerance=±5% resistance=220 package=THT]
  Part1 = Arduino Ethernet Shield (Rev3)
  LED1 = RGB LED (com. cathode, rgb) [package="5 mm [THT]"]

nets:
  N1: R1.Pin_0, LED1.common_cathode
  N2: R1.Pin_1, Part1.GND
  N3: Part1.PWM_D9, LED1.red_anode
  N4: Part1.ETH_CS, LED1.blue_anode
  N5: Part1.PWM_D11, LED1.green_anode
