# Fritzing sketch id1758_Fritzing_Amplifier2907_0 (saved by Fritzing 0.8.0b)
breadboards: 1

parts:
  IC1 = SO08 [chip_label=IC part_number=TDA7052A package=SO]
  R1 = Resistor [tolerance=±5% resistance=4.7k package="0805 [SMD]"]
  R2 = Resistor [tolerance=±5% resistance=470k package="0805 [SMD]"]
  R3 = Resistor [tolerance=±5% resistance=220 package="0805 [SMD]"]
  D1 = Rectifier Diode [part_number=1N4001 package="Melf DO-213 AB [SMD]"]
  C2 = Ceramic Capacitor [capacitance=100nF package="0805 [SMD, multilayer]"]
  C3 = Ceramic Capacitor [capacitance=100nF package="0805 [SMD, multilayer]"]
  LED1 = smd LED [color="Blue (470nm)" package="1206 [SMD]"]
  C4 = Ceramic Capacitor [capacitance=100nF package="0805 [SMD, multilayer]"]
  R4 = Resistor [tolerance=±5% resistance=4.7k package="0805 [SMD]"]
  SPKR1 = Loudspeaker
  J2 = female pin header, 2 pins [form="♀ (female)"]
  J1 = female pin header, 3 pins [form="♀ (female)"]
  C1 = Electrolytic Capacitor [capacitance=221µF voltage=50V package="1010 [SMD, electrolytic]"]

nets:
  N1: IC1.1, R3.Pin_1, D1.cathode, C1.+
  N2: IC1.2, C2.0, C4.1
  GND: IC1.3, IC1.6, R1.Pin_0, R2.Pin_1, C3.0, LED1.cathode, R4.Pin_0, J2.pin2, J1.pin2, C1.-
  N3: IC1.4, R2.Pin_0, C3.1
  N4: IC1.5, SPKR1.pin2
  N5: IC1.8, SPKR1.pin1
  N6: R1.Pin_1, C2.1, J1.pin1
  N7: R3.Pin_0, LED1.anode
  N8: D1.anode, J2.pin1
  N9: C4.0, R4.Pin_1, J1.pin3

notes:
  Fritzing Amplifier, Active Speaker for experiments and MP3 Player, _ A
  Fritzing Amplifier
  Powersupply from 5V to 15 V
  Connect here your earphone plug
  or your experiment.
  Right and left chanel are seperatet through C2 and C4.
  With R2 you can set the amplification. Range from cero ohm to 1 Megaohm.
  470 kOhm I've tested and it is good for MP3 or earphone connector.
  Fritzing Amplifier
  for Breadboard connect.
  I always wonder when people contact an 8 ohm loudspeaker direct to the microcontroller pin.
  When we calculate the current through the speaker we get :
  I=U/R= 5V/8 ohm=0,625A=625 mA
  But microcontroller pin can only drive 20 mA to 40 mA!!!
  So I designed this little amplifier to solve this problem.
  Now you can connect your experiment or your MP3-Player to Fritzing Amplifier and enjoy the sound, depending on speaker you connect.
  Have a lot of fun!
  Yours Michael J.
  L
  R
  Gnd
  PWR
  J2 Jack for powersupply from 5V to 15V.
  J1 Jack for sound input from your experiment or your MP3 Player L for left R for right Gnd for Ground.
  SPKR1 for Loudspeaker polarity independent.
