# Fritzing sketch id175_7Segment_LED_radioshack2_0 (saved by Fritzing 0.7.12b)
breadboards: 1

parts:
  Arduino1 = Arduino
  7_Segment1 = 7 Segment Display
  R1 = Resistor [tolerance=±5% resistance=150 package=THT]
  R2 = Resistor [tolerance=±5% resistance=150 package=THT]
  R3 = Resistor [tolerance=±5% resistance=150 package=THT]
  R4 = Resistor [tolerance=±5% resistance=150 package=THT]
  R5 = Resistor [tolerance=±5% resistance=150 package=THT]
  R6 = Resistor [tolerance=±5% resistance=150 package=THT]
  R7 = Resistor [tolerance=±5% resistance=150 package=THT]
  R8 = Resistor [tolerance=±5% resistance=150 package=THT]

nets:
  N1: Arduino1.GND, 7_Segment1.common_cathode
  N2: Arduino1.D9, R8.Pin_1
  N3: Arduino1.D8, R4.Pin_0
  N4: Arduino1.D7, R3.Pin_0
  N5: Arduino1.D6, R2.Pin_1
  N6: Arduino1.D5, R1.Pin_1
  N7: Arduino1.D4, R7.Pin_1
  N8: Arduino1.D3, R6.Pin_0
  N9: Arduino1.D2, R5.Pin_0
  N10: 7_Segment1.Segment_A#1, R3.Pin_1
  N11: 7_Segment1.Segment_F, R4.Pin_1
  N12: 7_Segment1.Segment_E, R2.Pin_0
  N13: 7_Segment1.Segment_D, R1.Pin_0
  N14: 7_Segment1.Segment_DP, R7.Pin_0
  N15: 7_Segment1.Segment_C, R8.Pin_0
  N16: 7_Segment1.Segment_B, R6.Pin_1
  N17: 7_Segment1.Segment_A#10, R5.Pin_1
