# Fritzing sketch id1763_Fortuneteller_0 (saved by Fritzing 0.8.3b)
circuit board: 6.88561cm x 5.36311cm
breadboards: 2

parts:
  R1 = Resistor [tolerance=±5% resistance=100k package=THT]
  Ja_aber_mit_Stil! = LED - 5mm [color="Blue (505nm)" package="5 mm [THT]"]
  R2 = Resistor [tolerance=±5% resistance=220 package=THT]
  R3 = Resistor [tolerance=±5% resistance=220 package=THT]
  R4 = Resistor [tolerance=±5% resistance=220 package=THT]
  Nein_lieber_nicht = LED - 5mm [color="Red (633nm)" package="5 mm [THT]"]
  Folge_deinem_Herzen = LED - 5mm [color="Green (555nm)" package="5 mm [THT]"]
  Warte_noch_etwas_damit = LED - 5mm [color="Yellow (585nm)" package="5 mm [THT]"]
  Unbedingt!_Sofort! = LED - 5mm [color="Blue (505nm)" package="5 mm [THT]"]
  Tilt = Tilt Switch [package=THT]
  R5 = Resistor [tolerance=±5% resistance=220 package=THT]
  R6 = Resistor [tolerance=±5% resistance=220 package=THT]
  Arduino1 = Arduino Uno (Rev3)

nets:
  N1: R1.Pin_0, Tilt.Pin_2, Arduino1.D3_PWM
  N2: R1.Pin_1, Arduino1.5V
  N3: Ja_aber_mit_Stil!.cathode, Nein_lieber_nicht.cathode, Folge_deinem_Herzen.cathode, Warte_noch_etwas_damit.cathode, Unbedingt!_Sofort!.cathode, Tilt.Pin_1, Arduino1.GND
  N4: Ja_aber_mit_Stil!.anode, R2.Pin_0
  N5: R2.Pin_1, Arduino1.D12/MISO
  N6: R3.Pin_0, Nein_lieber_nicht.anode
  N7: R3.Pin_1, Arduino1.D11_PWM/MOSI
  N8: R4.Pin_0, Folge_deinem_Herzen.anode
  N9: R4.Pin_1, Arduino1.D10_PWM/SS
  N10: Warte_noch_etwas_damit.anode, R5.Pin_0
  N11: Unbedingt!_Sofort!.anode, R6.Pin_0
  N12: R5.Pin_1, Arduino1.D9_PWM
  N13: R6.Pin_1, Arduino1.D8
