# Fritzing sketch id1765_Nightlight_0 (saved by Fritzing 0.8.3b)
breadboards: 2

parts:
  R1 = Resistor [tolerance=±5% resistance=220 package=THT]
  R2 = Resistor [tolerance=±5% resistance=220 package=THT]
  R3 = Resistor [tolerance=±5% resistance=220 package=THT]
  R4 = Rotary Potentiometer (Small) [maximum_resistance=100kΩ]
  Bauteil1 = Arduino Uno (Rev3)
  LED2 = RGB LED (com. cathode, rbg) [package="5 mm [THT]"]

nets:
  N1: R1.Pin_0, Bauteil1.D11_PWM/MOSI
  N2: R1.Pin_1, LED2.red_anode
  N3: R2.Pin_0, Bauteil1.D10_PWM/SS
  N4: R2.Pin_1, LED2.blue_anode
  N5: R3.Pin_0, Bauteil1.D9_PWM
  N6: R3.Pin_1, LED2.green_anode
  N7: R4.leg1, Bauteil1.GND, LED2.common_cathode
  N8: R4.wiper, Bauteil1.A0
  N9: R4.leg2, Bauteil1.5V
