# Fritzing sketch id176_Scoreboard_0 (saved by Fritzing 0.9.0b)
breadboards: 1

parts:
  7_Segment1 = 7 Segment Display
  IC1 = ULN2003A [package="DIP16 [THT]"]
  Q1 = NPN-Transistor [package="TO92 [THT]"]
  Power_plug1 = Power plug
  Onderdeel1 = Arduino Uno (Rev3)

nets:
  N1: 7_Segment1.Segment_G, IC1.Out_7
  N2: 7_Segment1.Segment_F, IC1.Out_6
  N3: 7_Segment1.common_anode, Q1.E
  N4: 7_Segment1.Segment_E, IC1.Out_5
  N5: 7_Segment1.Segment_D, IC1.Out_4
  N6: 7_Segment1.Segment_C, IC1.Out_3
  N7: 7_Segment1.Segment_B, IC1.Out_2
  N8: 7_Segment1.Segment_A, IC1.Out_1
  N9: IC1.In_1, Onderdeel1.D7
  N10: IC1.In_2, Onderdeel1.D8
  N11: IC1.In_3, Onderdeel1.D9_PWM
  N12: IC1.In_4, Onderdeel1.D10_PWM/SS
  N13: IC1.In_5, Onderdeel1.D11_PWM/MOSI
  N14: IC1.In_6, Onderdeel1.D12/MISO
  N15: IC1.In_7, Onderdeel1.D13/SCK
  GND: IC1.COM_-_Common, Power_plug1.GND, Onderdeel1.GND
  N16: Q1.B, Onderdeel1.D0/RX
  N17: Q1.C, Power_plug1.VCC
