# Fritzing sketch id1771_Servo_0 (saved by Fritzing 0.8.3b)
circuit board: 6.88561cm x 5.36311cm
breadboards: 2

parts:
  Servo = Basic Servo
  Bauteil1 = Arduino Uno (Rev3)
  Potentiometer = Rotary Potentiometer (Small)

nets:
  GND: Servo.gnd, Bauteil1.GND, Potentiometer.leg1
  VCC: Servo.vcc, Bauteil1.5V, Potentiometer.leg2
  N1: Servo.pulse, Bauteil1.D9_PWM
  N2: Bauteil1.A0, Potentiometer.wiper

notes:
  orange
  red
  brown
