# Fritzing sketch id1772_Synthesizer_0 (saved by Fritzing 0.8.3b)
breadboards: 2

parts:
  R3 = Resistor [tolerance=±5% resistance=220 package=THT]
  R2 = Rotary Potentiometer (Small)
  R1 = Rotary Potentiometer (Small)
  Arduino1 = Arduino Uno (Rev3)
  SG1 = sparkfun-electromechanical-buzzer-ns.fzp

nets:
  N1: R3.Pin_0, SG1.connector0
  N2: R3.Pin_1, R2.leg1, R1.leg1, Arduino1.GND
  N3: R2.wiper, Arduino1.A0
  N4: R2.leg2, R1.leg2, Arduino1.5V
  N5: R1.wiper, Arduino1.A1
  N6: Arduino1.D8, SG1.connector1
