# Fritzing sketch id1774_Zaubertafel_0 (saved by Fritzing 0.8.0b)
breadboards: 2

parts:
  R4 = Rotary Potentiometer (Small) [maximum_resistance=100kΩ]
  R5 = Rotary Potentiometer (Small) [maximum_resistance=100kΩ]
  S1 = Tilt Switch [package=THT]
  R6 = Resistor [tolerance=±5% resistance=100k package=THT]
  Bauteil1 = Arduino Uno (Rev3)

nets:
  N1: R4.leg1, R5.leg1, S1.Pin_1, Bauteil1.GND
  N2: R4.wiper, Bauteil1.A0
  N3: R4.leg2, R5.leg2, R6.Pin_1, Bauteil1.5V
  N4: R5.wiper, Bauteil1.A1
  N5: S1.Pin_2, R6.Pin_0, Bauteil1.D2
