# Fritzing sketch id1775_TwitterSaurus_0 (saved by Fritzing 0.8.0b)
breadboards: 2

parts:
  Servo = Basic Servo
  Bauteil1 = Arduino Uno (Rev3)

nets:
  GND: Servo.gnd, Bauteil1.GND
  VCC: Servo.vcc, Bauteil1.5V
  N1: Servo.pulse, Bauteil1.D9_PWM
