# Fritzing sketch id1776_KeyFobICSP_0 (saved by Fritzing 0.8.7b)
circuit board: 1.6121cm x 3.63538cm
perfboards: 1

parts:
  J1 = male pin header, 14 pins [form="♂ (male)"]
  J2 = male pin header, 14 pins [form="♂ (male)"]
  ICSP = male pin header, 3 pins [form="♂ (male)"]
  J4 = male pin header, 3 pins [form="♂ (male)"]

nets:
  N1: J1.pin10, ICSP.pin2
  N2: J1.pin11, ICSP.pin3
  N3: J1.pin12, J4.pin2
  N4: J2.pin1, ICSP.pin1
  N5: J2.pin7, J4.pin3
  N6: J2.pin8, J4.pin1

notes:
  +
  GND
