# Fritzing sketch id1777_CountingKnob_0 (saved by Fritzing 0.7.6b)
breadboards: 1

parts:
  Arduino1 = Arduino
  7_Segment1 = 7 Segment Display
  RE1 = Rotary Encoder [package=THT]

nets:
  N1: Arduino1.D13, 7_Segment1.Segment_B
  N2: Arduino1.D12, 7_Segment1.Segment_A
  N3: Arduino1.D11, 7_Segment1.common_anode
  N4: Arduino1.D10, 7_Segment1.Segment_F
  N5: Arduino1.D9, 7_Segment1.Segment_G
  N6: Arduino1.D5, 7_Segment1.Segment_E
  N7: Arduino1.D4, 7_Segment1.Segment_D
  N8: Arduino1.D3, 7_Segment1.Segment_C
  N9: Arduino1.D2, 7_Segment1.Segment_DP
  N10: Arduino1.GND, RE1.EncoderPinC
  N11: Arduino1.A0, RE1.EncoderPinB
  N12: Arduino1.A1, RE1.EncoderPinA
