# Fritzing sketch id1779_FRITZING_CONTADOR_UNO_AL_NUEVE_CARDENAS_0 (saved by Fritzing 0.9.3b)
breadboards: 1

parts:
  7_Segment1 = 7 Segment Display
  R1 = Resistor [tolerance=±5% resistance=330 package=THT]
  R2 = Resistor [tolerance=±5% resistance=330 package=THT]
  R3 = Resistor [tolerance=±5% resistance=330 package=THT]
  R4 = Resistor [tolerance=±5% resistance=330 package=THT]
  R5 = Resistor [tolerance=±5% resistance=330 package=THT]
  R6 = Resistor [tolerance=±5% resistance=330 package=THT]
  R7 = Resistor [tolerance=±5% resistance=330 package=THT]
  Componente1 = Arduino Uno (Rev3)

nets:
  N1: 7_Segment1.Segment_A#1, 7_Segment1.Segment_F, R1.Pin_1, R2.Pin_1
  N2: 7_Segment1.common_cathode, Componente1.GND
  N3: 7_Segment1.Segment_E, R3.Pin_1
  N4: 7_Segment1.Segment_D, R4.Pin_1
  N5: 7_Segment1.Segment_C, R6.Pin_0
  N6: 7_Segment1.Segment_B, 7_Segment1.Segment_A#10, R5.Pin_0, R7.Pin_0
  N7: R1.Pin_0, Componente1.D7
  N8: R2.Pin_0, Componente1.D8
  N9: R3.Pin_0, Componente1.D6_PWM
  N10: R4.Pin_0, Componente1.D5_PWM
  N11: R5.Pin_1, Componente1.D3_PWM
  N12: R6.Pin_1, Componente1.D4
  N13: R7.Pin_1, Componente1.D2
