# Fritzing sketch id1780_fritzingTCC1_0 (saved by Fritzing 0.8.3b)
circuit board: 9.5cm x 8cm
breadboards: 1

parts:
  R1 = Resistor [tolerance=±5% resistance=220 package=THT]
  R2 = Resistor [tolerance=±5% resistance=220 package=THT]
  R3 = Resistor [tolerance=±5% resistance=220 package=THT]
  R4 = Resistor [tolerance=±5% resistance=220 package=THT]
  LED1 = Super Flux LED blue [color=Blue]
  LED2 = LED - 5mm [color="Red (633nm)" package="5 mm [THT]"]
  LED3 = LED - 5mm [color="Green (570nm)" package="5 mm [THT]"]
  J1 = Basic Servo
  Adafruit_Atmega32u1 = Adafruit Atmega32u4 Breakout Board [part_number="Atmega 32u4"]
  J2 = Piezo Speaker
  Componente1 = RFID USB Reader
  U1 = GAS_SENSOR [package=mq-3]

nets:
  N1: R1.Pin_0, LED2.anode
  N2: R1.Pin_1, Adafruit_Atmega32u1.B1
  N3: R2.Pin_0, LED3.anode
  N4: R2.Pin_1, Adafruit_Atmega32u1.B2
  N5: R3.Pin_0, LED1.anode
  N6: R3.Pin_1, Adafruit_Atmega32u1.B3
  N7: R4.Pin_0, Adafruit_Atmega32u1.F0, U1.H1
  GND: R4.Pin_1, LED1.cathode, LED2.cathode, LED3.cathode, J1.gnd, Adafruit_Atmega32u1.GND#14, Componente1.GND, U1.H2
  VCC: J1.vcc, Adafruit_Atmega32u1.VCC, Componente1.VCC, U1.B1, U1.A1
  N8: J1.pulse, Adafruit_Atmega32u1.D0
  N9: Adafruit_Atmega32u1.B7, Componente1.ANT1
  N10: Adafruit_Atmega32u1.B6, Componente1.ANT2
  N11: Adafruit_Atmega32u1.B5, Componente1.CP
  N12: Adafruit_Atmega32u1.B4, Componente1.GNDT
  N13: Adafruit_Atmega32u1.B0, J2.pin2
  N14: Adafruit_Atmega32u1.D5, Componente1.TX-O
  N15: Adafruit_Atmega32u1.D6, Componente1.TX-O-RS232
  N16: Adafruit_Atmega32u1.GND#36, J2.pin1
