# Fritzing sketch id1782_Fritzuino_0 (saved by Fritzing 0.8.5b)
circuit board: 6.88566cm x 5.36311cm
breadboards: 1

parts:
  ATMEGA328P-PU1 = atmega328 [package=dip]
  J4 = female pin header, 8 pins [form="♀ (female)"]
  J5 = female pin header, 6 pins [form="♀ (female)"]
  J7 = female pin header, 6 pins [form="♀ (female)"]
  J6 = female pin header, 8 pins [form="♀ (female)"]
  Power_plug1 = Power plug
  S1 = Pushbutton [package="[THT]"]
  U1 = Voltage Regulator - 5V [part_number=LM7805 package="TO220 [THT]"]
  XTAL1 = Crystal [frequency="16 Mhz" package=THT]
  C6 = Ceramic Capacitor [capacitance=22pF package="200 mil [THT, multilayer]"]
  C7 = Ceramic Capacitor [capacitance=22pF package="200 mil [THT, multilayer]"]
  C3 = Ceramic Capacitor [capacitance=100nF package="200 mil [THT, multilayer]"]
  C4 = Ceramic Capacitor [capacitance=100nF package="200 mil [THT, multilayer]"]
  R3 = Resistor [tolerance=±5% resistance=10k package=THT]
  D1 = Rectifier Diode [part_number=1N4001 package="300 mil [THT]"]
  C8 = Electrolytic Capacitor [capacitance=47µF voltage=25V package="100 mil [THT, electrolytic]"]
  C9 = Electrolytic Capacitor [capacitance=47µF voltage=25V package="100 mil [THT, electrolytic]"]
  J3 = female pin header, 3 pins [form="♀ (female)"]
  LED2 = LED - 3mm [color="Green (555nm)" package="3 mm [THT]"]
  R2 = Resistor [tolerance=±5% resistance=330 package=THT]
  C2 = Ceramic Capacitor [capacitance=100nF package="200 mil [THT, multilayer]"]
  C5 = Ceramic Capacitor [capacitance=100nF package="200 mil [THT, multilayer]"]
  C1 = Ceramic Capacitor [capacitance=100nF package="200 mil [THT, multilayer]"]
  U2 = PNP-Transistor [part_number=MCP1700-3302E package="TO92 [THT]"]
  J2 = female pin header, 3 pins [form="♀ (female)"]
  R1 = Resistor [tolerance=±5% resistance=330 package=THT]
  LED1 = LED - 3mm [color="Red (633nm)" package="3 mm [THT]"]
  J1 = male pin header, 6 pins [form="♂ (male)"]
  J8 = double row male pin header, 6 pins [form="♂ (male)"]

nets:
  N1: ATMEGA328P-PU1.RESET, J5.pin1, S1.Pin_1, S1.Pin_2, R3.Pin_1, C1.1, J2.pin1, J8.pin3
  N2: ATMEGA328P-PU1.D0_(RX), J6.pin8, J1.pin3
  N3: ATMEGA328P-PU1.D1_(TX), J6.pin7, J1.pin2
  N4: ATMEGA328P-PU1.D2, J6.pin6
  N5: ATMEGA328P-PU1.D3_(PWM), J6.pin5
  N6: ATMEGA328P-PU1.D4, J6.pin4
  N7: ATMEGA328P-PU1.VCC, ATMEGA328P-PU1.AVCC, J5.pin3, C3.1, C4.0, R3.Pin_0, C9.+, J3.pin2, U2.B, LED1.anode, J8.pin6
  GND: ATMEGA328P-PU1.GND, J4.pin2, J5.pin4, J5.pin5, Power_plug1.GND, S1.Pin_3, S1.Pin_4, U1.GND, C6.1, C7.1, C3.0, C4.1, D1.anode, C8.-, C9.-, R2.Pin_0, C2.1, C5.1, U2.E, R1.Pin_1, J1.pin5, J1.pin6, J8.pin4
  N8: ATMEGA328P-PU1.XLAT1, XTAL1.pin_1, C7.0
  N9: ATMEGA328P-PU1.XLAT2, XTAL1.pin_0, C6.0
  N10: ATMEGA328P-PU1.D5_(PWM), J6.pin3
  N11: ATMEGA328P-PU1.D6_(PWM), J6.pin2
  N12: ATMEGA328P-PU1.D7, J6.pin1
  N13: ATMEGA328P-PU1.D8, J4.pin8
  N14: ATMEGA328P-PU1.D9_(PWM), J4.pin7
  N15: ATMEGA328P-PU1.D10_(PWM), J4.pin6
  N16: ATMEGA328P-PU1.D11_(PWM), J4.pin5, J8.pin5
  N17: ATMEGA328P-PU1.D12, J4.pin4, J8.pin1
  N18: ATMEGA328P-PU1.D13, J4.pin3, LED2.anode, J8.pin2
  N19: ATMEGA328P-PU1.AREF, J4.pin1, C5.0
  N20: ATMEGA328P-PU1.A0, J7.pin1
  N21: ATMEGA328P-PU1.A1, J7.pin2
  N22: ATMEGA328P-PU1.A2, J7.pin3
  N23: ATMEGA328P-PU1.A3, J7.pin4
  N24: ATMEGA328P-PU1.A4, J7.pin5
  N25: ATMEGA328P-PU1.A5, J7.pin6
  N26: J5.pin2, C2.0, U2.C
  N27: J5.pin6, Power_plug1.VCC, U1.input_voltage, D1.cathode, C8.+
  N28: U1.output_voltage, J3.pin3
  N29: J3.pin1, J1.pin4
  N30: LED2.cathode, R2.Pin_1
  N31: C1.0, J2.pin3
  N32: J2.pin2, J1.pin1
  N33: R1.Pin_0, LED1.cathode

notes:
  0
  1
  2
  3~
  4
  5~
  6~
  7
  8
  9~
  10~
  11~
  12
  13
  GND
  AREF
  A0
  A1
  A2
  A3
  A4
  A5
  DTR
  TX
  RX
  VCC
  USB
  EXT
  RST
  3.3V
  5.0V
  VIN
  <-----------DIGITAL---------->
  <--ANALOG-->
  Fritzuino
  ICSP
  ATMEGA328P-PU
