# Fritzing sketch id1783_HPCUTOUT_0 (saved by Fritzing 0.3.14b)
breadboards: 1

parts:
  J1 = Basic Force Sensing Resistor (FSR) [package=THT]
  BATT = obsolete Battery
  R1 = Resistor [resistance=220 package=THT]
  R2 = Resistor [resistance=220 package=THT]
  OFF = Red LED - 5mm
  ON = green LED - 5mm

nets:
  N1: J1.pin_0, ON.cathode
  N2: J1.pin_1, R1.Pin_1, R2.Pin_0
  N3: BATT.-, R1.Pin_0
  N4: BATT.+, OFF.anode, ON.anode
  N5: R2.Pin_1, OFF.cathode

notes:
  THIS DESIGN SIMULATES A HIGH-PRESSURE CUT-OUT ON A REFRIGERATING DEVICE. PRESSURE BUILDS ON THE FSR AND WHEN IT HITS ENOUGH IT TURNS OFF THE GREEN LED AND TURNS ON THE RED LED.
