# Fritzing sketch id1784_FSR_LED_Series_0 (saved by Fritzing 0.9.1b)
breadboards: 1

parts:
  Part1 = Arduino Uno (Rev3)
  J1 = Basic Force Sensing Resistor (FSR) [package=THT]
  LED1 = LED - 5mm [color="Red (633nm)" package="5 mm [THT]"]
  LED2 = LED - 5mm [color="Red (633nm)" package="5 mm [THT]"]
  LED3 = LED - 5mm [color="Red (633nm)" package="5 mm [THT]"]
  LED4 = LED - 5mm [color="Red (633nm)" package="5 mm [THT]"]
  LED5 = LED - 5mm [color="Red (633nm)" package="5 mm [THT]"]
  R1 = Resistor [tolerance=±5% resistance=220 package=THT]
  R2 = Resistor [tolerance=±5% resistance=220 package=THT]
  R3 = Resistor [tolerance=±5% resistance=220 package=THT]
  R4 = Resistor [tolerance=±5% resistance=220 package=THT]
  R5 = Resistor [tolerance=±5% resistance=220 package=THT]
  R6 = Resistor [tolerance=±5% resistance=220 package=THT]

nets:
  N1: Part1.A0, J1.pin_1, R2.Pin_1
  N2: Part1.D9_PWM, LED1.cathode
  N3: Part1.D10_PWM/SS, LED2.cathode
  N4: Part1.D11_PWM/MOSI, LED3.cathode
  N5: Part1.D12/MISO, LED4.cathode
  N6: Part1.D13/SCK, LED5.cathode
  N7: Part1.5V, R1.Pin_0, R2.Pin_0, R3.Pin_0, R4.Pin_0, R5.Pin_0, R6.Pin_0
  N8: Part1.GND, J1.pin_0
  N9: LED1.anode, R6.Pin_1
  N10: LED2.anode, R5.Pin_1
  N11: LED3.anode, R4.Pin_1
  N12: LED4.anode, R3.Pin_1
  N13: LED5.anode, R1.Pin_1
