# Fritzing sketch id1785_fsrFirstTest_0 (saved by Fritzing 0.7.4b)
breadboards: 1

parts:
  U1 = Arduino Mega
  J1 = Basic Force Sensing Resistor (FSR) [package=THT]
  R1 = Resistor [tolerance=±5% resistance=10k package=THT]

nets:
  N1: U1.+5V, J1.pin_1
  N2: U1.GND, R1.Pin_0
  N3: U1.A0, J1.pin_0, R1.Pin_1
