# Fritzing sketch id1787_SQUAWK_TRANSPONDER_0 (saved by Fritzing 0.8.7b)
circuit board: 16.9333cm x 5.64444cm
breadboards: 1

parts:
  LCD1 = LCD screen
  R3 = Resistor [tolerance=±5% resistance=10k package=THT]
  R4 = Resistor [tolerance=±5% resistance=10k package=THT]
  R5 = Resistor [tolerance=±5% resistance=10k package=THT]
  R6 = Resistor [tolerance=±5% resistance=10k package=THT]
  R7 = Resistor [tolerance=±5% resistance=10k package=THT]
  R8 = Resistor [tolerance=±5% resistance=10k package=THT]
  R9 = Resistor [tolerance=±5% resistance=10k package=THT]
  R10 = Resistor [tolerance=±5% resistance=10k package=THT]
  R11 = Resistor [tolerance=±5% resistance=10k package=THT]
  R12 = Resistor [tolerance=±5% resistance=10k package=THT]
  R13 = Resistor [tolerance=±5% resistance=10k package=THT]
  R14 = Resistor [tolerance=±5% resistance=10k package=THT]
  R15 = Resistor [tolerance=±5% resistance=10k package=THT]
  R16 = Resistor [tolerance=±5% resistance=10k package=THT]
  S1 = Pushbutton [package="[THT]"]
  S2 = Pushbutton [package="[THT]"]
  S3 = Pushbutton [package="[THT]"]
  S4 = Pushbutton [package="[THT]"]
  S5 = Pushbutton [package="[THT]"]
  S6 = Pushbutton [package="[THT]"]
  S7 = Pushbutton [package="[THT]"]
  S8 = Pushbutton [package="[THT]"]
  S9 = Pushbutton [package="[THT]"]
  THE_ROTARY_SWITCH = mystery part, 6 pins [chip_label="ROTARY SWITCH"]
  R17 = Resistor [tolerance=±5% resistance=220 package=THT]
  LED_Zero_Button = LED - 5mm [color="Red (633nm)" package="5 mm [THT]"]
  LED_One_Button = LED - 5mm [color="Red (633nm)" package="5 mm [THT]"]
  LED_Two_Button = LED - 5mm [color="Red (633nm)" package="5 mm [THT]"]
  LED_Three_Button = LED - 5mm [color="Red (633nm)" package="5 mm [THT]"]
  LED_Four_Button = LED - 5mm [color="Red (633nm)" package="5 mm [THT]"]
  LED_Five_Button = LED - 5mm [color="Red (633nm)" package="5 mm [THT]"]
  LED_Six_Button = LED - 5mm [color="Red (633nm)" package="5 mm [THT]"]
  LED_Seven_Button = LED - 5mm [color="Red (633nm)" package="5 mm [THT]"]
  LED_VFR_Button = LED - 5mm [color="Red (633nm)" package="5 mm [THT]"]
  S10 = Pushbutton [package="[THT]"]
  S11 = Pushbutton [package="[THT]"]
  LED_IDT_Button = LED - 5mm [color="Red (633nm)" package="5 mm [THT]"]
  LED_CLR_Button = LED - 5mm [color="Red (633nm)" package="5 mm [THT]"]
  R2 = Rotary Potentiometer (Small) [maximum_resistance=5kΩ package=THT]
  R1 = Rotary Potentiometer (Small) [maximum_resistance=5kΩ package=THT]
  U1 = Arduino Mega 2560 (Rev3)

nets:
  VSS: LCD1.VSS, LCD1.R/W, LCD1.LED-, R3.Pin_1, R4.Pin_1, R5.Pin_1, R6.Pin_1, R7.Pin_1, R8.Pin_1, R9.Pin_1, R10.Pin_1, R11.Pin_1, R12.Pin_1, R13.Pin_1, R14.Pin_1, R15.Pin_1, R16.Pin_1, R17.Pin_1, R2.leg2, R1.leg2, U1.GND
  N1: LCD1.VDD, S1.Pin_3, S1.Pin_4, S2.Pin_3, S2.Pin_4, S3.Pin_3, S3.Pin_4, S4.Pin_3, S4.Pin_4, S5.Pin_3, S5.Pin_4, S6.Pin_3, S6.Pin_4, S7.Pin_3, S7.Pin_4, S8.Pin_3, S8.Pin_4, S9.Pin_3, S9.Pin_4, THE_ROTARY_SWITCH.pin6, S10.Pin_3, S10.Pin_4, S11.Pin_3, S11.Pin_4, R2.leg1, R1.leg1
  N2: LCD1.V0, R1.wiper
  N3: LCD1.RS, U1.D27
  N4: LCD1.E, U1.D26
  N5: LCD1.DB4, U1.D25
  N6: LCD1.DB5, U1.D24
  N7: LCD1.DB6, U1.D23
  N8: LCD1.DB7, U1.D22
  N9: LCD1.LED+, R2.wiper
  N10: R3.Pin_0, S1.Pin_1, S1.Pin_2, LED_Zero_Button.anode, U1.D28
  N11: R4.Pin_0, S2.Pin_1, S2.Pin_2, LED_One_Button.anode, U1.D29
  N12: R5.Pin_0, S3.Pin_1, S3.Pin_2, LED_Two_Button.anode, U1.D30
  N13: R6.Pin_0, S4.Pin_1, S4.Pin_2, LED_Three_Button.anode, U1.D31
  N14: R7.Pin_0, S5.Pin_1, S5.Pin_2, LED_Four_Button.anode, U1.D32
  N15: R8.Pin_0, S6.Pin_1, S6.Pin_2, LED_Five_Button.anode, U1.D33
  N16: R9.Pin_0, S7.Pin_1, S7.Pin_2, LED_Six_Button.anode, U1.D35
  N17: R10.Pin_0, S8.Pin_1, S8.Pin_2, LED_Seven_Button.anode, U1.D34
  N18: R11.Pin_0, S9.Pin_1, S9.Pin_2, LED_VFR_Button.anode, U1.D36
  N19: R12.Pin_0, THE_ROTARY_SWITCH.pin1, U1.D37
  N20: R13.Pin_0, THE_ROTARY_SWITCH.pin2, U1.D38
  N21: R14.Pin_0, THE_ROTARY_SWITCH.pin3, U1.D39
  N22: R15.Pin_0, THE_ROTARY_SWITCH.pin4, U1.D40
  N23: R16.Pin_0, THE_ROTARY_SWITCH.pin5, U1.D41
  N24: R17.Pin_0, LED_Zero_Button.cathode, LED_One_Button.cathode, LED_Two_Button.cathode, LED_Three_Button.cathode, LED_Four_Button.cathode, LED_Five_Button.cathode, LED_Six_Button.cathode, LED_Seven_Button.cathode, LED_VFR_Button.cathode, LED_IDT_Button.cathode, LED_CLR_Button.cathode
  N25: S10.Pin_1, S10.Pin_2, LED_IDT_Button.anode
  N26: S11.Pin_1, S11.Pin_2, LED_CLR_Button.anode

notes:
  Adjust Basklight
  Adjust Contrast
  R 1 = Adjust LCD Contrast = 5 KOhm
  R 2 = Adjust LCD Backlight = 5 KOhm
  R 3 = "Zero" Button = 10 KOhm
  R 4 = "One" Button = 10 KOhm
  R 5 = "Two" Button = 10 KOhm
  R 6 = "Three" Button = 10 KOhm
  R 7 = "Four" Button = 10 KOhm
  R 8 = "Five" Button = 10 KOhm
  R 9 = "Six" Button = 10 KOhm
  R 10 = "Seven" Button = 10 KOhm
  R 11 = "VFR" Button = 10 KOhm
  R12 = Rotary Switch "OFF" Pin = 10 KOhm
  R13 = Rotary Switch "SBY" Pin = 10 KOhm
  R14 = Rotary Switch "TST" Pin = 10 KOhm
  R 15 = Rotary Switch "ON" Pin = 10 KOhm
  R 16 = Rotary Switch "ALT" Pin = 10 KOhm
  R 17 = LED Resistor = 220 Ohm
  Resistor Diagram
  S 1 = Zero Button
  S 2 = One Button
  S 3 = Two Button
  S 4 = Three Button
  S 5 = Four Button
  S 6 = Five Button
  S 7 = Six Button
  S 8 = Seven Button
  S 9 = VFR Button
  S 10 = IDT Button "No Function"
  S11 = CLR Button "No Function"
  Button Switch diagram
  This wiring diagram is for making "DIY" Squawk Code Transponder.
  It is for sending Squawk codes to Microsoft Flight Simulator X.
  It uses Jim NZ's program, Link2fs, as an interpreter between the transponder and FSX.
  Sketch/Code and info, is to be found at:
  MyCockpit Forum, Arduino Cards & Link2FS,
  Tread: Arduino input & output.
  http://www.mycockpit.org/forums/arduino-cards-link2fs/26161-arduino-input-output.html
  Wiring Diagram made by
  --------BuzziBi----------
  08.05.2013
  XPNDR STANDBY MODE
  ALT 110 SQUAWK 1200
