# Fritzing sketch id1788_FSX__MCP_0 (saved by Fritzing 0.9.2b)
circuit board: 12.7138cm x 7.50538cm
breadboards: 1

parts:
  Composant1 = Arduino Uno (Rev3)
  S2 = Pushbutton [package="[THT]"]
  S3 = Pushbutton [package="[THT]"]
  R1 = Rotary Potentiometer (Small) [maximum_resistance=100kΩ package=THT]
  R2 = Resistor [tolerance=±5% resistance=220 package=THT]
  R3 = Resistor [tolerance=±5% resistance=220 package=THT]
  R4 = Resistor [tolerance=±5% resistance=4.7k package=THT]
  J1 = Piezo Speaker
  R5 = Resistor [tolerance=±5% resistance=100 package=THT]
  LCD1 = LCD screen
  S1 = Pushbutton [package="[THT]"]
  R7 = Resistor [tolerance=±5% resistance=7.5 package=THT]
  R8 = Resistor [tolerance=±5% resistance=220 package=THT]
  LED1 = LED - 5mm [color="Red (633nm)" package="5 mm [THT]"]

nets (from the breadboard view):
  N1: Composant1.A0, R1.wiper
  N2: Composant1.D8, LCD1.DB7
  N3: Composant1.D9_PWM, LCD1.DB6
  N4: Composant1.D10_PWM/SS, LCD1.DB5
  N5: Composant1.D11_PWM/MOSI, LCD1.DB4
  N6: Composant1.D12/MISO, LCD1.E
  N7: Composant1.D13/SCK, LCD1.RS
  GND: Composant1.GND, R1.leg1, R2.Pin_0, R3.Pin_0, R4.Pin_0, J1.pin1, LCD1.VSS, LCD1.LED-, R7.Pin_0
  5V: Composant1.D2, Composant1.D3_PWM, Composant1.D4, Composant1.5V, S2.Pin_1, S2.Pin_2, S3.Pin_1, S3.Pin_2, R1.leg2, LCD1.VDD, S1.Pin_1, S1.Pin_2, R8.Pin_0, LED1.anode
  N8: Composant1.D6_PWM, R5.Pin_0
  N9: Composant1.D7, LED1.cathode
  N10: S2.Pin_3, S2.Pin_4, R3.Pin_1
  N11: S3.Pin_3, S3.Pin_4, R2.Pin_1
  N12: R4.Pin_1, S1.Pin_3, S1.Pin_4
  N13: J1.pin2, R5.Pin_1
  N14: LCD1.V0, R7.Pin_1
  N15: LCD1.LED+, R8.Pin_1
