# Fritzing sketch id1789_USB_TO_TTL_ESP8226_0 (saved by Fritzing 0.9.2b)
circuit board: 2.07628cm x 3.39083cm
breadboards: 1

parts:
  ESP8266 = ESP8266_module_2 [part_number=ESP8266]
  RX = Header 1 [package=1x01_offset]
  VC = Header 1 [package=1x01_offset]
  TX = Header 1 [package=1x01_offset]
  GND = Header 1 [package=1x01_offset]
  C2 = Tantalum Capacitor [capacitance=10µF voltage=10V package="B 3528 [SMD, tantalum]"]
  C1 = Tantalum Capacitor [capacitance=10µF voltage=20V package="B 3528 [SMD, tantalum]"]
  R5 = Resistor [tolerance=±5% resistance=1k package=THT]
  R6 = Resistor [tolerance=±5% resistance=2k package=THT]
  1117_3_3V = LM1117DTX-3.3 
  R7 = Resistor [tolerance=±5% resistance=10k package=THT]
  VC1 = Header 1 [package=1x01_offset]  # not connected
  VC2 = Header 1 [package=1x01_offset]  # not connected

nets:
  N1: ESP8266.connector0, R5.Pin_0, R6.Pin_0
  N2: ESP8266.connector1, C2.+, 1117_3_3V.connector1, 1117_3_3V.connector3, R7.Pin_0
  N3: ESP8266.connector5, R7.Pin_1
  N4: ESP8266.connector6, GND.1, C2.-, C1.-, R6.Pin_1, 1117_3_3V.connector0
  N5: ESP8266.connector7, RX.1
  N6: VC.1, C1.+, 1117_3_3V.connector2
  N7: TX.1, R5.Pin_1
