# Fritzing sketch id178_HC595_ATTiny_0 (saved by Fritzing 0.9.0b)
circuit board: 6cm x 3.2cm
breadboards: 1

parts:
  ATTiny = attiny85 [package=dip]
  74HC595 = 74HC595 [package="DIP16 [THT]"]
  VCC2 = Battery block 9V
  U4 = Voltage Regulator - 5V [package="TO220 [THT]"]
  U10 = mystery part, 3 pins [chip_label=Serial]
  U11 = mystery part, 3 pins [chip_label=Serial]
  U9 = mystery part, 3 pins [chip_label=Serial]
  U12 = mystery part, 16 pins [chip_label=Serial]
  U13 = mystery part, 3 pins [chip_label=Serial]
  VCC4 = Battery block 9V

nets:
  N1: ATTiny.Pin_1, U9.pin3
  N2: ATTiny.Pin_2, 74HC595.SH_CP
  N3: ATTiny.Pin_3, 74HC595.ST_CP
  GND: ATTiny.Pin_4, 74HC595.GND, 74HC595.OE, VCC2.-, U4.GND, U10.pin1, U11.pin1, U9.pin1, U12.pin2, U12.pin4, U12.pin6, U12.pin8, U12.pin10, U12.pin12, U12.pin14, U12.pin16, U13.pin1, VCC4.-
  N4: ATTiny.Pin_5, U10.pin3
  N5: ATTiny.Pin_6, U11.pin3
  N6: ATTiny.Pin_7, 74HC595.DS
  N7: ATTiny.Pin_8, 74HC595.MR, 74HC595.VCC, U4.output_voltage, U10.pin2, U11.pin2, U9.pin2, U13.pin2, VCC4.+
  N8: 74HC595.Q1, U12.pin3
  N9: 74HC595.Q2, U12.pin5
  N10: 74HC595.Q3, U12.pin7
  N11: 74HC595.Q4, U12.pin9
  N12: 74HC595.Q5, U12.pin11
  N13: 74HC595.Q6, U12.pin13
  N14: 74HC595.Q7, U12.pin15
  N15: 74HC595.Q7', U13.pin3
  N16: 74HC595.Q0, U12.pin1
  N17: VCC2.+, U4.input_voltage

notes:
  9 volt in
  Ground
  VCC
  40
  20
  10
  08
  04
  02
  01
  80
  Reset
  Pin 0
  Pin 1
  Serial
  5 volt out
  Data
  Knowledge And Technology Joyfully Engaged
  W.A. ten Brink
