# Fritzing sketch id1790_Focio_0 (saved by Fritzing 0.9.3b)
breadboards: 1

parts:
  R1 = Resistor [tolerance=±5% resistance=220 package=THT]  # not connected
  Componente1 = Triple Axis Accelerometer Breakout - ADXL335
  RE1 = Rotary Encoder [package=THT]
  J1 = Basic Force Sensing Resistor (FSR) [package=THT]
  ANT1 = Antenna
  U1 = QRD1114 [package=qrd1114]
  R2 = Resistor [tolerance=±5% resistance=220 package=THT]
  R3 = Resistor [tolerance=±5% resistance=220 package=THT]
  R4 = Resistor [tolerance=±5% resistance=220 package=THT]

nets:
  N1: Componente1.ZOUT, R3.Pin_1
  N2: Componente1.YOUT, R4.Pin_0
  N3: Componente1.XOUT, R3.Pin_0
  N4: Componente1.GND, RE1.EncoderPinB, R4.Pin_1
  N5: J1.pin_1, ANT1.antenna_lead, U1.K
  N6: U1.E, R2.Pin_0
  N7: U1.A, R2.Pin_1
