# Fritzing sketch id1791_current_setup_0 (saved by Fritzing 0.9.2b)
breadboards: 1

parts:
  Part1 = Arduino Uno (Rev3)  # not connected
  R1 = Resistor [tolerance=±5% resistance=220 package=THT]
  LED1 = smd LED [color="Red (633nm)" package="0603 [SMD]"]  # not connected
  ANT1 = Antenna

nets:
  N1: R1.Pin_1, ANT1.antenna_lead

notes:
  wall circuit strip
  LED light strip running a 375ma 16 v adapter ->>
  magnetic lock running on a ac110-240v input and outputs up to 12v 3a Images in email
  relay
