# Fritzing sketch id179_555_Timer_IC (saved by Fritzing 0.6.3b)
breadboards: 1

parts:
  U1 = 555 Timer [package="DIP8 [THT]"]
  VCC1 = Battery
  R1 = Resistor [tolerance=±5% resistance=1k package=THT]
  LED1 = LED - 5mm [color="Red (633nm)" package="5 mm [THT]"]
  C1 = Electrolytic Capacitor [capacitance=1µF package="100 mil [THT, electrolytic]"]
  R2 = Resistor [tolerance=±5% resistance=1k package=THT]

nets:
  N1: U1.Ground, VCC1.-, LED1.cathode, C1.-
  N2: U1.Trigger, U1.Threshold, C1.+, R2.Pin_1
  N3: U1.Output, LED1.anode
  N4: U1.Reset, U1.Vcc_Supply_Voltage, VCC1.+, R1.Pin_1
  N5: U1.Discharge, R1.Pin_0, R2.Pin_0

notes:
  555 Timer LED Flasher
  555 Timer LED Flasher
  You may change the speed of flashing by simple replace the C1 with bigger value like 1000uF
  By Adeel Rizvi
