# Fritzing sketch id179_devreSemasi_0 (saved by Fritzing 0.9.3b)
breadboards: 2

parts:
  U1 = 74HC595 [package="DIP16 [THT]"]
  Parça1 = Arduino Uno (Rev3) - ICSP
  LED1 = smd LED [color="Red (633nm)" package="1206 [SMD]"]
  LED2 = smd LED [color="Red (633nm)" package="1206 [SMD]"]
  LED3 = smd LED [color="Red (633nm)" package="1206 [SMD]"]
  LED4 = smd LED [color="Red (633nm)" package="1206 [SMD]"]
  LED5 = smd LED [color="Green (570nm)" package="1206 [SMD]"]
  LED6 = smd LED [color="Green (570nm)" package="1206 [SMD]"]
  LED7 = smd LED [color="Green (570nm)" package="1206 [SMD]"]
  LED8 = smd LED [color="Green (570nm)" package="1206 [SMD]"]
  R1 = Resistor [tolerance=±5% resistance=220 package="0603 [SMD]"]
  R2 = Resistor [tolerance=±5% resistance=220 package="0603 [SMD]"]
  R3 = Resistor [tolerance=±5% resistance=220 package="0603 [SMD]"]
  R5 = Resistor [tolerance=±5% resistance=220 package="0603 [SMD]"]
  R6 = Resistor [tolerance=±5% resistance=220 package="0603 [SMD]"]
  R7 = Resistor [tolerance=±5% resistance=220 package="0603 [SMD]"]
  R8 = Resistor [tolerance=±5% resistance=220 package="0603 [SMD]"]
  R9 = Resistor [tolerance=±5% resistance=220 package="0603 [SMD]"]

nets:
  N1: U1.Q1, R2.Pin_1
  N2: U1.Q2, R3.Pin_1
  N3: U1.Q3, R5.Pin_1
  N4: U1.Q4, R6.Pin_1
  N5: U1.Q5, R7.Pin_1
  N6: U1.Q6, R8.Pin_1
  N7: U1.Q7, R9.Pin_1
  GND: U1.GND, U1.OE, Parça1.GND
  VCC: U1.MR, U1.VCC, Parça1.5V, LED1.anode, LED2.anode, LED3.anode, LED4.anode, LED5.anode, LED6.anode, LED7.anode, LED8.anode
  N8: U1.SH_CP, Parça1.D11_PWM/MOSI
  N9: U1.ST_CP, Parça1.D12/MISO
  N10: U1.DS, Parça1.D13/SCK
  N11: U1.Q0, R1.Pin_1
  N12: LED1.cathode, R1.Pin_0
  N13: LED2.cathode, R2.Pin_0
  N14: LED3.cathode, R3.Pin_0
  N15: LED4.cathode, R5.Pin_0
  N16: LED5.cathode, R6.Pin_0
  N17: LED6.cathode, R9.Pin_0
  N18: LED7.cathode, R7.Pin_0
  N19: LED8.cathode, R8.Pin_0
