# Fritzing sketch id17_010_butonla_led_yakma_pull_down_0 (saved by Fritzing 0.9.2b)
breadboards: 1

parts:
  Eleman1 = Arduino Uno (Rev3)
  S1 = Pushbutton [package=THT]
  R1 = Resistor [tolerance=±5% resistance=10k package=THT]
  R2 = Resistor [tolerance=±5% resistance=220 package=THT]
  LED1 = LED - 5mm [color="Red (633nm)" package="5 mm [THT]"]

nets:
  N1: Eleman1.D3_PWM, R2.Pin_1
  N2: Eleman1.D4, S1.leg1, R1.Pin_1
  N3: Eleman1.GND, S1.leg0, R1.Pin_0, LED1.cathode
  N4: R2.Pin_0, LED1.anode
