# Fritzing sketch id1802_Fun_MOOC_Arduino___TP4___Sketch_0 (saved by Fritzing 0.9.2b)
breadboards: 1

parts:
  J1 = Basic Servo
  Composant1 = Arduino Uno (Rev3)
  S1 = Pushbutton [package="[THT]"]
  R1 = Resistor [tolerance=±5% resistance=10k package=THT]
  LED1 = LED - 5mm [color="Red (633nm)" package="5 mm [THT]"]
  LED2 = LED - 5mm [color="Green (565nm)" package="5 mm [THT]"]
  R2 = Resistor [tolerance=±5% resistance=220 package=THT]
  R3 = Resistor [tolerance=±5% resistance=220 package=THT]

nets:
  GND: J1.gnd, Composant1.GND, R1.Pin_1, R2.Pin_1, R3.Pin_1
  VCC: J1.vcc, Composant1.5V, S1.Pin_3, S1.Pin_4
  N1: J1.pulse, Composant1.D9_PWM
  N2: Composant1.D10_PWM/SS, LED1.anode
  N3: Composant1.D11_PWM/MOSI, LED2.anode
  N4: Composant1.D2, S1.Pin_1, S1.Pin_2, R1.Pin_0
  N5: LED1.cathode, R2.Pin_0
  N6: LED2.cathode, R3.Pin_0
