# Fritzing sketch id1804_FunctionGenerator_0 (saved by Fritzing 0.9.2b)
circuit board: 8.46667cm x 5.64444cm
breadboards: 1

parts:
  U1 = LMV324 [package=so014]
  BAT1 = BC9VPC [package=bc9vpc]
  C1 = Ceramic Capacitor [capacitance=1µF voltage=9V package="200 mil [THT, multilayer]"]
  R1 = Resistor [tolerance=±5% resistance=22k package=THT]
  R2 = Resistor [tolerance=±5% resistance=10k package=THT]
  R3 = Resistor [tolerance=±5% resistance=100k package=THT]
  R4 = Resistor [tolerance=±5% resistance=10k package=THT]
  R5 = Rotary Potentiometer (Small) [maximum_resistance=100kΩ package=THT]
  R6 = Resistor [tolerance=±5% resistance=100k package=THT]
  R7 = Resistor [tolerance=±5% resistance=100k package=THT]
  R8 = Resistor [tolerance=±5% resistance=100k package=THT]
  C2 = Ceramic Capacitor [capacitance=100nF voltage=9V package="100 mil [THT, multilayer]"]
  C3 = Ceramic Capacitor [capacitance=100nF voltage=9V package="100 mil [THT, multilayer]"]

nets:
  N1: U1.G$1_OUT, R2.Pin_1
  N2: U1.G$1_-IN, C1.1, R5.wiper
  N3: U1.G$1_+IN, R1.Pin_1, R6.Pin_0
  N4: U1.G$1_+V, BAT1.V+, R5.leg2
  N5: U1.G$2_+IN, R4.Pin_0
  N6: U1.G$2_-IN, R2.Pin_0, R6.Pin_1, R8.Pin_0, C2.0
  N7: U1.G$2_OUT, R7.Pin_0, R8.Pin_1, C2.1
  N8: U1.G$3_OUT, C3.1
  N9: U1.G$3_-IN, R7.Pin_1, C3.0
  N10: U1.G$3_+IN, R3.Pin_1
  N11: U1.G$1_-V, BAT1.V-, C1.0, R1.Pin_0, R3.Pin_0, R4.Pin_1, R5.leg1
