# Fritzing sketch id1804_estazio_metereologikoa (saved by Fritzing 0.9.3b)
breadboards: 1

parts:
  Componente1 = Arduino Uno (Rev3)
  Componente2 = Bluetooth HC-05 Macho
  R1 = Photocell (LDR) [package=THT]
  R2 = Resistor [tolerance=±5% resistance=10k package="0402 [SMD]"]
  RHT1 = Humidity and Temperature Sensor RHT03
  R3 = Resistor [tolerance=±5% resistance=10k package="0402 [SMD]"]

nets:
  N1: Componente1.A0, R1.pin_1, R2.Pin_1
  N2: Componente1.D0/RX, Componente2.TXD
  N3: Componente1.D1/TX, Componente2.RXD
  N4: Componente1.D5_PWM, RHT1.Data-signal, R3.Pin_1
  VCC: Componente1.5V, Componente2.VCC, R1.pin_0, RHT1.Vcc, R3.Pin_0
  GND: Componente1.GND, Componente2.GND, R2.Pin_0, RHT1.GND_1
