# Fritzing sketch id1806_GMLT_0 (saved by Fritzing 0.8.7b)
circuit board: 9cm x 5.4cm
breadboards: 2

parts:
  LCDContrast = Rotary Potentiometer (Small) [maximum_resistance=100kΩ package=THT]
  LED = RGB LED (com. anode, rbg) [package="5 mm [THT]"]
  R1_R2_R3_LED_RGB = Resistor [tolerance=±5% resistance=220 package=THT]
  R1 = Resistor [tolerance=±5% resistance=220 package=THT]
  R2 = Resistor [tolerance=±5% resistance=220 package=THT]
  FSR = Basic Force Sensing Resistor (FSR) [package=THT]
  R7_FSR = Resistor [resistance=10k tolerance=±5% package=THT]
  R4_LCD_Blue = Resistor [tolerance=±5% resistance=220 package=THT]
  R5_LCD_Green = Resistor [tolerance=±5% resistance=220 package=THT]
  R6_LCD_Red = Resistor [tolerance=±5% resistance=220 package=THT]
  LCD_18_17 = female pin header, 2 pins [form="♀ (female)"]
  LCD = LCD screen
  Galileo = Arduino Leonardo (Rev3b)
  VCC_SCL = female pin header, 2 pins [form="♀ (female)"]
  SDA = female pin header, 2 pins [form="♀ (female)"]
  ADR0_ADR1 = female pin header, 2 pins [form="♀ (female)"]  # not connected
  GND = female pin header, 2 pins [form="♀ (female)"]

nets:
  VSS: LCDContrast.leg1, R7_FSR.Pin_0, LCD.VSS, LCD.R/W, Galileo.GND, GND.pin1
  N1: LCDContrast.wiper, LCD.V0
  VDD: LCDContrast.leg2, LED.common_anode, FSR.pin_0, LCD.VDD, LCD.LED+, Galileo.5V, VCC_SCL.pin1
  N2: LED.red_cathode, R1_R2_R3_LED_RGB.Pin_0
  N3: LED.blue_cathode, R1.Pin_0
  N4: LED.green_cathode, R2.Pin_0
  N5: R1_R2_R3_LED_RGB.Pin_1, Galileo.A1
  N6: R1.Pin_1, Galileo.A2
  N7: R2.Pin_1, Galileo.A3
  N8: FSR.pin_1, R7_FSR.Pin_1, Galileo.A0
  N9: R4_LCD_Blue.Pin_0, Galileo.D9_PWM/A9
  N10: R4_LCD_Blue.Pin_1, LCD_18_17.pin1
  N11: R5_LCD_Green.Pin_0, Galileo.D10_PWM/A10
  N12: R5_LCD_Green.Pin_1, LCD_18_17.pin2
  N13: R6_LCD_Red.Pin_0, Galileo.D11_PWM
  N14: R6_LCD_Red.Pin_1, LCD.LED-
  N15: LCD.RS, Galileo.D3_PWM/SCL, Galileo.SCL, VCC_SCL.pin2
  N16: LCD.E, Galileo.D4/A6
  N17: LCD.DB4, Galileo.D5_PWM
  N18: LCD.DB5, Galileo.D6_PWM/A7
  N19: LCD.DB6, Galileo.D7
  N20: LCD.DB7, Galileo.D8/A8
  N21: Galileo.D2/SDA, Galileo.SDA, SDA.pin1

notes:
  GMLT THE F11x Galileo Project https://communities.intel.com/message/218943
