# Fritzing sketch id1807_galileo_0 (saved by Fritzing 0.9.3b)
circuit board: 2.19017cm x 4.86922cm

parts:
  J8 = Basic Servo
  J3 = Basic Servo
  J1 = Basic Servo
  J2 = Basic Servo
  J10 = Basic Servo
  J7 = Basic Servo
  Part1 = Arduino Mega 2560 (Rev3)
  J4 = Basic Servo
  J6 = Basic Servo
  J9 = Basic Servo
  J5 = Basic Servo
  J11 = Screw terminal - 2 pins [package=THT]
  J12 = Basic Servo
  J13 = Basic Servo

nets:
  GND: J8.gnd, J3.gnd, J1.gnd, J2.gnd, J10.gnd, J7.gnd, Part1.GND, J4.gnd, J6.gnd, J9.gnd, J5.gnd, J11.pin1, J12.gnd, J13.gnd
  VCC: J8.vcc, J3.vcc, J1.vcc, J2.vcc, J10.vcc, J7.vcc, J4.vcc, J6.vcc, J9.vcc, J5.vcc, J11.pin2, J12.vcc, J13.vcc
  N1: J8.pulse, Part1.D51
  N2: J3.pulse, Part1.D27
  N3: J1.pulse, Part1.D23
  N4: J2.pulse, Part1.D25
  N5: J10.pulse, Part1.D47
  N6: J7.pulse, Part1.D45
  N7: Part1.D29, J4.pulse
  N8: Part1.D31, J5.pulse
  N9: Part1.D35, J13.pulse
  N10: Part1.D37, J12.pulse
  N11: Part1.D49, J9.pulse
  N12: Part1.D53, J6.pulse

notes:
  -
  LEFT
  RIGHT
  H
  A
  D
  E
