# Fritzing sketch id1808_fritz_DataMonsterCircuitry_fritzing_0 (saved by Fritzing 0.8.8b)
circuit board: 5.36514cm x 7.14954cm
breadboards: 2

parts:
  R1 = Resistor [tolerance=±5% resistance=220 package=THT]
  LED1 = LED - 5mm [color="Red (633nm)" part_number=pin04 package="5 mm [THT]"]
  R2 = Resistor [tolerance=±5% resistance=220 package=THT]
  LED2 = LED - 5mm [color="Yellow (585nm)" part_number=pin07 package="5 mm [THT]"]
  R3 = Resistor [tolerance=±5% resistance=220 package=THT]
  LED3 = LED - 5mm [color="Green (560nm)" part_number=pin08 package="5 mm [THT]"]
  S1 = Pushbutton [package="[THT]"]
  R4 = Resistor [tolerance=±5% resistance=10k package=THT]
  C1 = Ceramic Capacitor [capacitance=10µF package="100 mil [THT, multilayer]"]
  Power_plug1 = Power plug [part_number=powersupply]
  J1 = Basic Servo [part_number=pin05]
  J2 = Basic Servo [part_number=pin06]
  J3 = Basic Servo [part_number=pin09]
  J4 = Basic Servo [part_number="pin 10"]
  J5 = Basic Servo [part_number=pin11]
  J6 = Infrared Proximity Sensor [part_number=A0]
  J7 = Infrared Proximity Sensor [part_number=A1]
  J8 = Infrared Proximity Sensor [part_number=A2]
  Part1 = Intel Galileo

nets:
  N1: R1.Pin_0, LED1.cathode
  GND: R1.Pin_1, R2.Pin_1, R3.Pin_1, R4.Pin_1, C1.0, Power_plug1.GND, J1.gnd, J2.gnd, J3.gnd, J4.gnd, J5.gnd, J6.GND, J7.GND, J8.GND, Part1.GND
  N2: LED1.anode, Part1.D4
  N3: R2.Pin_0, LED2.cathode
  N4: LED2.anode, Part1.D7
  N5: R3.Pin_0, LED3.cathode
  N6: LED3.anode, Part1.D8
  VCC: S1.Pin_1, S1.Pin_2, R4.Pin_0, C1.1, J6.Vcc, J7.Vcc, J8.Vcc, Part1.5V
  N7: S1.Pin_3, S1.Pin_4, Part1.D2
  VCC_2: Power_plug1.VCC, J1.vcc, J2.vcc, J3.vcc, J4.vcc, J5.vcc
  N8: J1.pulse, Part1.D5_PWM
  N9: J2.pulse, Part1.D6_PWM
  N10: J3.pulse, Part1.D9_PWM
  N11: J4.pulse, Part1.D10_PWM/SS
  N12: J5.pulse, Part1.D11_PWM/MOSI
  N13: J6.Vout, Part1.A0
  N14: J7.Vout, Part1.A1
  N15: J8.Vout, Part1.A2

notes:
  <_________servo-connections________>
  <__________distance________>
  dataMonster
  ***0.1***
