# Fritzing sketch id1809_gameController_0 (saved by Fritzing 0.9.3b)
breadboards: 1

parts:
  Part1 = Arduino Micro (Rev3)
  S1 = Pushbutton [package="[THT]"]
  S2 = Pushbutton [package="[THT]"]
  S3 = Pushbutton [package="[THT]"]
  S4 = Pushbutton [package="[THT]"]
  S5 = Pushbutton [package="[THT]"]
  R1 = Resistor [tolerance=±5% resistance=10k package=THT]
  R2 = Resistor [tolerance=±5% resistance=10k package=THT]
  R3 = Resistor [tolerance=±5% resistance=10k package=THT]
  R4 = Resistor [tolerance=±5% resistance=10k package=THT]
  R5 = Resistor [tolerance=±5% resistance=10k package=THT]

nets:
  N1: Part1.D2/SDA, S3.Pin_3, S3.Pin_4, R2.Pin_1
  N2: Part1.D3/SCL, S2.Pin_3, S2.Pin_4, R1.Pin_1
  N3: Part1.D4_PWM/A6, S5.Pin_3, S5.Pin_4, R3.Pin_1
  N4: Part1.D5_PWM, S4.Pin_3, S4.Pin_4, R4.Pin_1
  N5: Part1.D8_PWM/A8, S1.Pin_3, S1.Pin_4, R5.Pin_1
  N6: Part1.GND, R1.Pin_0, R2.Pin_0, R3.Pin_0, R4.Pin_0, R5.Pin_0
  N7: Part1.5V, S1.Pin_1, S1.Pin_2, S2.Pin_1, S2.Pin_2, S3.Pin_1, S3.Pin_2, S4.Pin_1, S4.Pin_2, S5.Pin_1, S5.Pin_2
