# Fritzing sketch id1810_GAMELINES_0 (saved by Fritzing 0.9.0b)
circuit board: 6.444cm x 10.4309cm
breadboards: 1

parts:
  Attiny85 = attiny85 [package=dip]
  470K = Resistor [tolerance=±5% resistance=47k package=THT]
  7805 = Voltage Regulator - 5V [package="TO220 [THT]"]
  10K = Rotary Potentiometer (Large) [maximum_resistance=100kΩ package=THT]
  switch = Toggle Switch [package=THT]
  -9V+ = Battery block 9V
  220 = Resistor [tolerance=±5% resistance=220 package=THT]
  LED = LED - 5mm [color="Red (633nm)" package="5 mm [THT]"]
  LM386 = IC, DIP package, 8 pins [chip_label=LM386]
  10K_2 = Rotary Potentiometer (Large) [maximum_resistance=100kΩ package=THT]
  10uF = Electrolytic Capacitor [capacitance=1µF package="100 mil [THT, electrolytic]"]
  100uF = Electrolytic Capacitor [capacitance=4.7µF package="100 mil [THT, electrolytic]"]
  +SPKR- = Loudspeaker
  U7 = electrodo_Mandala
  D1 = Rectifier Diode [part_number=1N4001 package="300 mil [THT]"]
  -line_out+ = female pin header, 2 pins [form="♀ (female)"]

nets:
  N1: Attiny85.Pin_2, 10K.wiper
  N2: Attiny85.Pin_3, 470K.Pin_0, U7.connector0
  GND: Attiny85.Pin_4, 470K.Pin_1, 7805.GND, 10K.leg2, -9V+.-, 220.Pin_1, LM386.pin2, LM386.pin4, 10K_2.leg2, +SPKR-.pin2, -line_out+.pin2
  N3: Attiny85.Pin_5, 10uF.+
  N4: Attiny85.Pin_8, 7805.output_voltage, 10K.leg1, LED.anode, U7.connector3
  N5: 7805.input_voltage, switch.L1, LM386.pin6
  N6: switch.COM, D1.cathode
  N7: -9V+.+, D1.anode
  N8: 220.Pin_0, LED.cathode
  N9: LM386.pin3, 10K_2.wiper, -line_out+.pin1
  N10: LM386.pin5, 100uF.+
  N11: 100uF.-, +SPKR-.pin1

notes:
  GAMELINES (léase en castellano), laboratoriodejuguete.com
