# Fritzing sketch id1811_GAMELIN_II_0 (saved by Fritzing 0.9.2b)
circuit board: 7.5cm x 10cm
breadboards: 1

parts:
  Attiny85/45_8mHz = attiny85 [package=dip]
  470K = Resistor [tolerance=±5% resistance=47k package=THT]
  LED = smd LED [color="Red (633nm)" package="0805 [SMD]"]
  10K = Rotary Potentiometer (Small) [maximum_resistance=10kΩ package=THT]
  10K_2 = Rotary Potentiometer (Small) [maximum_resistance=10kΩ package=THT]
  TRS1 = Audio Jack (TRS) 3.5mm [package="4Ucon 08780 [THT]"]
  220 = Resistor [tolerance=±5% resistance=2.2k package=THT]
  S1 = SWITCH-DPDT [package=eg2211]
  J1 = Piezo Speaker
  U3 = electrodo_Mandala_MINI
  CR2016 = Battery Holders [package=battcom_20mm_pth]

nets:
  N1: Attiny85/45_8mHz.Pin_2, 10K_2.wiper
  N2: Attiny85/45_8mHz.Pin_3, 470K.Pin_0, U3.connector3
  GND: Attiny85/45_8mHz.Pin_4, 10K.leg2, 10K_2.leg2, TRS1.Sleeve, 220.Pin_1, S1.5, J1.pin1, U3.connector0
  N3: Attiny85/45_8mHz.Pin_5, 10K.leg1
  N4: Attiny85/45_8mHz.Pin_8, 470K.Pin_1, LED.anode, 10K_2.leg1, CR2016.+
  N5: LED.cathode, 220.Pin_0
  N6: 10K.wiper, TRS1.Ring, TRS1.Tip, J1.pin2
  N7: S1.4, CR2016.-

notes:
  GAMELIN, laboratoriodejuguete.com
  MINI
