# Fritzing sketch id1812_gamingboard_0 (saved by Fritzing 0.8.5b)
breadboards: 1

parts:
  S1 = Pushbutton [package="[THT]"]
  S2 = Pushbutton [package="[THT]"]
  S3 = Pushbutton [package="[THT]"]
  R1 = Resistor [tolerance=±5% resistance=220 package=THT]
  R2 = Resistor [tolerance=±5% resistance=220 package=THT]
  Teensy_3_1 = Teensy 3.0
  Part1 = Thumb Joystick
  Part2 = Thumb Joystick
  S4 = Pushbutton [package="[THT]"]
  S5 = Pushbutton [package="[THT]"]
  S6 = Pushbutton [package="[THT]"]
  S7 = Pushbutton [package="[THT]"]
  S8 = Pushbutton [package="[THT]"]
  S9 = Pushbutton [package="[THT]"]
  S10 = Pushbutton [package="[THT]"]
  S11 = Pushbutton [package="[THT]"]
  S12 = Pushbutton [package="[THT]"]
  S13 = Pushbutton [package="[THT]"]
  R3 = Resistor [tolerance=±5% resistance=220 package=THT]
  R4 = Resistor [tolerance=±5% resistance=220 package=THT]
  R5 = Resistor [tolerance=±5% resistance=220 package=THT]
  R6 = Resistor [tolerance=±5% resistance=220 package=THT]
  R7 = Resistor [tolerance=±5% resistance=220 package=THT]
  R8 = Resistor [tolerance=±5% resistance=220 package=THT]
  R9 = Resistor [tolerance=±5% resistance=220 package=THT]
  R10 = Resistor [tolerance=±5% resistance=220 package=THT]
  R11 = Resistor [tolerance=±5% resistance=220 package=THT]
  R12 = Resistor [tolerance=±5% resistance=220 package=THT]
  R13 = Resistor [tolerance=±5% resistance=220 package=THT]

nets:
  N1: S1.Pin_1, S1.Pin_2, Teensy_3_1.D0
  VCC: S1.Pin_3, S1.Pin_4, S2.Pin_3, S2.Pin_4, S3.Pin_3, S3.Pin_4, R1.Pin_1, R2.Pin_1, Teensy_3_1.Vin, Part1.VCC, Part2.VCC, S4.Pin_3, S4.Pin_4, S5.Pin_3, S5.Pin_4, S6.Pin_3, S6.Pin_4, S7.Pin_3, S7.Pin_4, S8.Pin_3, S8.Pin_4, S9.Pin_3, S9.Pin_4, S10.Pin_3, S10.Pin_4, S11.Pin_3, S11.Pin_4, S12.Pin_3, S12.Pin_4, S13.Pin_3, S13.Pin_4, R3.Pin_1, R4.Pin_1, R5.Pin_1, R6.Pin_1, R7.Pin_1, R8.Pin_1, R9.Pin_1, R10.Pin_1, R11.Pin_1, R12.Pin_1, R13.Pin_1
  N2: S2.Pin_1, S2.Pin_2
  N3: S3.Pin_1, S3.Pin_2, Teensy_3_1.D1
  GND: R1.Pin_0, R2.Pin_0, Teensy_3_1.GND, Part1.GND, Part2.GND, R3.Pin_0, R4.Pin_0, R5.Pin_0, R6.Pin_0, R7.Pin_0, R8.Pin_0, R9.Pin_0, R10.Pin_0, R11.Pin_0, R12.Pin_0, R13.Pin_0
  N4: Teensy_3_1.D2, S4.Pin_1, S4.Pin_2
  N5: Teensy_3_1.A0/D14, Teensy_3_1.A5/D19, Part1.SEL, Part1.HORZ
  N6: Teensy_3_1.A1/D15, Part1.VERT
  N7: Teensy_3_1.A2/D16, Part2.HORZ
  N8: Teensy_3_1.A3/D17, Part2.VERT
  N9: Teensy_3_1.A4/D18, Part2.SEL
  N10: S5.Pin_1, S5.Pin_2
  N11: S6.Pin_1, S6.Pin_2
  N12: S7.Pin_1, S7.Pin_2
  N13: S8.Pin_1, S8.Pin_2
  N14: S9.Pin_1, S9.Pin_2
  N15: S10.Pin_1, S10.Pin_2
  N16: S11.Pin_1, S11.Pin_2
  N17: S12.Pin_1, S12.Pin_2
  N18: S13.Pin_1, S13.Pin_2
