# Fritzing sketch id181_7segment_button_fritzing_0 (saved by Fritzing 0.9.3b)
breadboards: 1

parts:
  부품1 = Arduino Uno (Rev3)
  R1 = Resistor [tolerance=±5% resistance=220 package=THT]
  7_Segment1 = 7 Segment Display
  R2 = Resistor [tolerance=±5% resistance=220 package=THT]
  R3 = Resistor [tolerance=±5% resistance=220 package=THT]
  R4 = Resistor [tolerance=±5% resistance=220 package=THT]
  R5 = Resistor [tolerance=±5% resistance=220 package=THT]
  R6 = Resistor [tolerance=±5% resistance=220 package=THT]
  R7 = Resistor [tolerance=±5% resistance=220 package=THT]
  R8 = Resistor [tolerance=±5% resistance=220 package=THT]
  S1 = Pushbutton [package="[THT]"]
  S2 = Pushbutton [package="[THT]"]
  R9 = Resistor [tolerance=±5% resistance=10k package="2010 [SMD]"]
  R10 = Resistor [tolerance=±5% resistance=10k package="2010 [SMD]"]

nets:
  N1: 부품1.D8, R5.Pin_0
  N2: 부품1.D9_PWM, R8.Pin_1
  N3: 부품1.D11_PWM/MOSI, S1.Pin_1, S1.Pin_2, R9.Pin_0
  N4: 부품1.D12/MISO, S2.Pin_1, S2.Pin_2, R10.Pin_0
  N5: 부품1.GND, R9.Pin_1, R10.Pin_1
  N6: 부품1.D2, R4.Pin_1
  N7: 부품1.D3_PWM, R3.Pin_1
  N8: 부품1.D4, R7.Pin_1
  N9: 부품1.D5_PWM, R2.Pin_0
  N10: 부품1.D6_PWM, R6.Pin_0
  N11: 부품1.D7, R1.Pin_0
  N12: 부품1.5V, 7_Segment1.common_anode, S1.Pin_3, S1.Pin_4, S2.Pin_3, S2.Pin_4
  N13: R1.Pin_1, 7_Segment1.Segment_F
  N14: 7_Segment1.Segment_E, R6.Pin_1
  N15: 7_Segment1.Segment_D, R2.Pin_1
  N16: 7_Segment1.Segment_C, R7.Pin_0
  N17: 7_Segment1.Segment_DP, R8.Pin_0
  N18: 7_Segment1.Segment_B, R3.Pin_0
  N19: 7_Segment1.Segment_A, R4.Pin_0
  N20: 7_Segment1.Segment_G, R5.Pin_1
