# Fritzing sketch id1820_Dual_Fade (saved by Fritzing 0.3.10b)
breadboards: 1

parts:
  Arduino1 = Arduino
  LED1 = Red LED - 5mm
  LED3 = yellow LED - 5mm
  R1 = Resistor [resistance=220 package=THT]
  R2 = Resistor [resistance=220 package=THT]

nets:
  N1: Arduino1.GND, LED1.cathode, LED3.cathode
  N2: Arduino1.D10, R2.Pin_0
  N3: Arduino1.D9, R1.Pin_1
  N4: LED1.anode, R1.Pin_0
  N5: LED3.anode, R2.Pin_1
