# Fritzing sketch id182_7segment_num_fritzing_0 (saved by Fritzing 0.9.3b)
breadboards: 1

parts:
  부품1 = Arduino Uno (Rev3)
  R1 = Resistor [tolerance=±5% resistance=220 package=THT]
  7_Segment1 = 7 Segment Display
  R2 = Resistor [tolerance=±5% resistance=220 package=THT]
  R3 = Resistor [tolerance=±5% resistance=220 package=THT]
  R4 = Resistor [tolerance=±5% resistance=220 package=THT]
  R5 = Resistor [tolerance=±5% resistance=220 package=THT]
  R6 = Resistor [tolerance=±5% resistance=220 package=THT]
  R7 = Resistor [tolerance=±5% resistance=220 package=THT]
  R8 = Resistor [tolerance=±5% resistance=220 package=THT]

nets:
  N1: 부품1.D8, R5.Pin_0
  N2: 부품1.D9_PWM, R8.Pin_1
  N3: 부품1.D2, R4.Pin_1
  N4: 부품1.D3_PWM, R3.Pin_1
  N5: 부품1.D4, R7.Pin_1
  N6: 부품1.D5_PWM, R2.Pin_0
  N7: 부품1.D6_PWM, R6.Pin_0
  N8: 부품1.D7, R1.Pin_0
  N9: 부품1.5V, 7_Segment1.common_anode
  N10: R1.Pin_1, 7_Segment1.Segment_F
  N11: 7_Segment1.Segment_E, R6.Pin_1
  N12: 7_Segment1.Segment_D, R2.Pin_1
  N13: 7_Segment1.Segment_C, R7.Pin_0
  N14: 7_Segment1.Segment_DP, R8.Pin_0
  N15: 7_Segment1.Segment_B, R3.Pin_0
  N16: 7_Segment1.Segment_A, R4.Pin_0
  N17: 7_Segment1.Segment_G, R5.Pin_1
