# Fritzing sketch id1838_Feedback_Tesla_Coil (saved by Fritzing 0.9.3b)
breadboards: 1

parts:
  U1 = Voltage Regulator - 5V [package="TO220 [THT]"]
  C1 = Electrolytic Capacitor [capacitance=47µF voltage=20V package="100 mil [THT, electrolytic]"]
  C2 = Electrolytic Capacitor [capacitance=47µF voltage=20V package="100 mil [THT, electrolytic]"]
  IC1 = SN74LS14N [package="DIP14 [THT]"]
  C3 = Electrolytic Capacitor [capacitance=1µF package="100 mil [THT, electrolytic]"]
  R1 = Resistor [tolerance=±5% resistance=470 package=THT]
  D1 = Rectifier Diode [part_number=1N4148 package="300 mil [THT]"]
  D2 = Rectifier Diode [part_number=1N4148 package="300 mil [THT]"]
  C4 = Electrolytic Capacitor [capacitance=100nF package="100 mil [THT, electrolytic]"]
  IC2 = IC, DIP package, 8 pins [chip_label=UCC37322]
  R2 = Resistor [tolerance=±5% resistance=470 package=THT]
  Q1 = Basic FET P-Channel [package="TO220 [THT]"]
  C6 = Electrolytic Capacitor [capacitance=1µF package="100 mil [THT, electrolytic]"]
  D3 = Schottky Diode [part_number=1N5819 breakdown_voltage=3.6V package="300 mil [THT]"]
  C7 = Ceramic Capacitor [capacitance=2.2µF package="100 mil [THT, multilayer]"]
  U2 = 555 Timer [package="DIP8 [THT]"]
  S1 = Toggle Switch [package=THT]
  C8 = Ceramic Capacitor [capacitance=100nF package="100 mil [THT, multilayer]"]
  C9 = Ceramic Capacitor [capacitance=100nF package="100 mil [THT, multilayer]"]
  R3 = Resistor [tolerance=±5% resistance=220 package=THT]
  R4 = Resistor [tolerance=±5% resistance=220 package=THT]
  R5 = Rotary Potentiometer (Small) [maximum_resistance=100kΩ package=THT]
  R6 = Rotary Potentiometer (Small) [maximum_resistance=100kΩ package=THT]
  D4 = Rectifier Diode [part_number=1N4001 package="300 mil [THT]"]
  D5 = Rectifier Diode [part_number=1N4001 package="300 mil [THT]"]

nets:
  12V: U1.input_voltage, C1.+, IC2.pin1, IC2.pin8
  GND: U1.GND, C1.-, C2.-, IC1.GND, D2.anode, C4.-, IC2.pin4, IC2.pin5, Q1.source, C6.-, C7.0, U2.Ground, U2.Discharge, C8.0, C9.0
  5V: U1.output_voltage, C2.+, IC1.VCC, D1.cathode, C4.+, U2.Reset, U2.Vcc_Supply_Voltage
  N1: IC1.5Y, IC2.pin2
  N2: IC1.5A, IC1.6Y
  N3: IC1.6A, R1.Pin_1, D1.anode, D2.cathode
  N4: C3.-, R1.Pin_0
  ANT: C3.+
  N5: IC2.pin3, S1.COM
  N6: IC2.pin6, IC2.pin7, R2.Pin_1, D3.cathode
  N7: R2.Pin_0, Q1.gate, D3.anode
  Primary: Q1.drain, C6.+, C7.1
  N8: U2.Trigger, C9.1
  N9: U2.Output, R3.Pin_0, R4.Pin_1
  N10: U2.Control_Voltage, C8.1
  N11: U2.Threshold, R5.wiper, R6.wiper
  외부_신호: S1.L1
  내부_인터럽트: S1.L2, R3.Pin_1
  N12: R4.Pin_0, D4.cathode, D5.anode
  N13: R5.leg1, D5.cathode
  N14: R6.leg1, D4.anode

notes:
  MMC
  MKP 10~680nF
