# Fritzing sketch id183_7x5led_0 (saved by Fritzing 0.9.1b)

parts:
  LED31 = LED - 5mm [color="White (4500K)" package="5 mm [THT]"]
  LED32 = LED - 5mm [color="White (4500K)" package="5 mm [THT]"]
  LED33 = LED - 5mm [color="White (4500K)" package="5 mm [THT]"]
  LED34 = LED - 5mm [color="White (4500K)" package="5 mm [THT]"]
  LED35 = LED - 5mm [color="White (4500K)" package="5 mm [THT]"]
  LED36 = LED - 5mm [color="White (4500K)" package="5 mm [THT]"]
  LED37 = LED - 5mm [color="White (4500K)" package="5 mm [THT]"]
  LED38 = LED - 5mm [color="White (4500K)" package="5 mm [THT]"]
  LED39 = LED - 5mm [color="White (4500K)" package="5 mm [THT]"]
  LED40 = LED - 5mm [color="White (4500K)" package="5 mm [THT]"]
  LED41 = LED - 5mm [color="White (4500K)" package="5 mm [THT]"]
  LED42 = LED - 5mm [color="White (4500K)" package="5 mm [THT]"]
  LED43 = LED - 5mm [color="White (4500K)" package="5 mm [THT]"]
  LED44 = LED - 5mm [color="White (4500K)" package="5 mm [THT]"]
  LED45 = LED - 5mm [color="White (4500K)" package="5 mm [THT]"]
  LED46 = LED - 5mm [color="White (4500K)" package="5 mm [THT]"]
  LED47 = LED - 5mm [color="White (4500K)" package="5 mm [THT]"]
  LED48 = LED - 5mm [color="White (4500K)" package="5 mm [THT]"]
  LED49 = LED - 5mm [color="White (4500K)" package="5 mm [THT]"]
  LED50 = LED - 5mm [color="White (4500K)" package="5 mm [THT]"]
  LED51 = LED - 5mm [color="White (4500K)" package="5 mm [THT]"]
  LED52 = LED - 5mm [color="White (4500K)" package="5 mm [THT]"]
  LED53 = LED - 5mm [color="White (4500K)" package="5 mm [THT]"]
  LED54 = LED - 5mm [color="White (4500K)" package="5 mm [THT]"]
  LED55 = LED - 5mm [color="White (4500K)" package="5 mm [THT]"]
  LED56 = LED - 5mm [color="White (4500K)" package="5 mm [THT]"]
  LED57 = LED - 5mm [color="White (4500K)" package="5 mm [THT]"]
  LED58 = LED - 5mm [color="White (4500K)" package="5 mm [THT]"]
  LED59 = LED - 5mm [color="White (4500K)" package="5 mm [THT]"]
  LED60 = LED - 5mm [color="White (4500K)" package="5 mm [THT]"]
  LED61 = LED - 5mm [color="White (4500K)" package="5 mm [THT]"]
  LED62 = LED - 5mm [color="White (4500K)" package="5 mm [THT]"]
  LED63 = LED - 5mm [color="White (4500K)" package="5 mm [THT]"]
  LED64 = LED - 5mm [color="White (4500K)" package="5 mm [THT]"]
  LED65 = LED - 5mm [color="White (4500K)" package="5 mm [THT]"]
  R1 = Resistor [tolerance=±5% resistance=220 package=THT]
  R2 = Resistor [tolerance=±5% resistance=220 package=THT]
  R3 = Resistor [tolerance=±5% resistance=220 package=THT]
  R4 = Resistor [tolerance=±5% resistance=220 package=THT]
  R5 = Resistor [tolerance=±5% resistance=220 package=THT]
  Bauteil1 = Arduino Uno (Rev3)

nets:
  N1: LED31.cathode, LED38.cathode, LED45.cathode, LED52.cathode, LED59.cathode, Bauteil1.D13/SCK
  N2: LED31.anode, LED32.anode, LED33.anode, LED34.anode, LED35.anode, LED36.anode, LED37.anode, R5.Pin_0
  N3: LED32.cathode, LED39.cathode, LED46.cathode
  N4: LED33.cathode, LED40.cathode, LED47.cathode, LED54.cathode, LED61.cathode, Bauteil1.D11_PWM/MOSI
  N5: LED34.cathode, LED41.cathode, LED48.cathode, LED55.cathode, LED62.cathode, Bauteil1.D10_PWM/SS
  N6: LED35.cathode, LED42.cathode, LED49.cathode, LED56.cathode, LED63.cathode, Bauteil1.D9_PWM
  N7: LED36.cathode, LED43.cathode, LED50.cathode
  N8: LED37.cathode, LED44.cathode, LED51.cathode, LED58.cathode, LED65.cathode, Bauteil1.D7
  N9: LED38.anode, LED39.anode, LED40.anode, LED41.anode, LED42.anode, LED43.anode, LED44.anode, R4.Pin_0
  N10: LED45.anode, LED46.anode, LED47.anode, LED48.anode, LED49.anode, LED50.anode, LED51.anode, R3.Pin_0
  N11: LED52.anode, LED53.anode, LED54.anode, LED55.anode, LED56.anode, LED57.anode, LED58.anode, R2.Pin_0
  N12: LED53.cathode, LED60.cathode, Bauteil1.D12/MISO
  N13: LED57.cathode, LED64.cathode, Bauteil1.D8
  N14: LED59.anode, LED60.anode, LED61.anode, LED62.anode, LED63.anode, LED64.anode, LED65.anode, R1.Pin_0
  N15: R1.Pin_1, Bauteil1.D6_PWM
  N16: R2.Pin_1, Bauteil1.D5_PWM
  N17: R3.Pin_1, Bauteil1.D4
  N18: R4.Pin_1, Bauteil1.D3_PWM
  N19: R5.Pin_1, Bauteil1.D2
