# Fritzing sketch id184_DontKnow_0 (saved by Fritzing 0.9.2b)
circuit board: 12.3444cm x 15.4268cm
breadboards: 2

parts:
  U1 = Optocoupler [package=THT]
  R9 = Resistor [tolerance=±5% resistance=220 package=THT]
  U3 = Optocoupler [package=THT]
  R10 = Resistor [tolerance=±5% resistance=220 package=THT]
  R11 = Resistor [tolerance=±5% resistance=220 package=THT]
  U4 = Optocoupler [package=THT]
  R12 = Resistor [tolerance=±5% resistance=220 package=THT]
  U2 = Optocoupler [package=THT]
  U5 = Optocoupler [package=THT]
  U6 = Optocoupler [package=THT]
  U7 = Optocoupler [package=THT]
  U8 = Optocoupler [package=THT]
  R13 = Resistor [tolerance=±5% resistance=220 package=THT]
  R14 = Resistor [tolerance=±5% resistance=220 package=THT]
  R15 = Resistor [tolerance=±5% resistance=220 package=THT]
  R16 = Resistor [tolerance=±5% resistance=220 package=THT]
  IC1 = Voltage Regulator [package=to-220-alt]
  R17 = Resistor [tolerance=±5% resistance=220 package=THT]
  IC2 = Voltage Regulator [package=to-220-alt]
  R18 = Resistor [tolerance=±5% resistance=220 package=THT]
  IC3 = Voltage Regulator [package=to-220-alt]
  R19 = Resistor [tolerance=±5% resistance=220 package=THT]
  IC4 = Voltage Regulator [package=to-220-alt]
  R20 = Resistor [tolerance=±5% resistance=220 package=THT]
  IC5 = Voltage Regulator [package=to-220-alt]
  R21 = Resistor [tolerance=±5% resistance=220 package=THT]
  IC6 = Voltage Regulator [package=to-220-alt]
  R22 = Resistor [tolerance=±5% resistance=220 package=THT]
  IC7 = Voltage Regulator [package=to-220-alt]
  R23 = Resistor [tolerance=±5% resistance=220 package=THT]
  IC8 = Voltage Regulator [package=to-220-alt]
  R24 = Resistor [tolerance=±5% resistance=220 package=THT]
  J1 = Screw terminal - 2 pins [package=THT]
  J2 = Screw terminal - 2 pins [package=THT]
  J3 = Screw terminal - 2 pins [package=THT]
  J4 = Screw terminal - 2 pins [package=THT]
  J5 = Screw terminal - 2 pins [package=THT]
  J6 = Screw terminal - 2 pins [package=THT]
  J7 = Screw terminal - 2 pins [package=THT]
  J8 = Screw terminal - 2 pins [package=THT]
  Part1 = Photon
  R25 = Resistor [tolerance=±5% resistance=220 package=THT]
  R26 = Resistor [tolerance=±5% resistance=220 package=THT]
  R27 = Resistor [tolerance=±5% resistance=220 package=THT]
  R28 = Resistor [tolerance=±5% resistance=220 package=THT]
  R29 = Resistor [tolerance=±5% resistance=220 package=THT]
  R30 = Resistor [tolerance=±5% resistance=220 package=THT]
  R31 = Resistor [tolerance=±5% resistance=220 package=THT]
  R32 = Resistor [tolerance=±5% resistance=220 package=THT]
  BAT2 = Battery Holders [package=battcon_12mm_pth]
  U10 = microSD Socket [package=usd-socket-pp]  # not connected

nets:
  N1: U1.Pin_1, R21.Pin_0
  N2: U1.Pin_2, IC5.GND, J4.pin1
  N3: U1.Pin_4, Part1.D7, R32.Pin_1
  N4: U1.Pin_5, R9.Pin_1
  3.3V: R9.Pin_0, R10.Pin_0, R11.Pin_0, R12.Pin_0, R13.Pin_0, R14.Pin_0, R15.Pin_0, R16.Pin_0, Part1.3V3
  N5: U3.Pin_1, R23.Pin_0
  N6: U3.Pin_2, IC7.GND, J2.pin1
  N7: U3.Pin_4, Part1.D3, R28.Pin_1
  N8: U3.Pin_5, R11.Pin_1
  N9: R10.Pin_1, U2.Pin_5
  N10: U4.Pin_1, R24.Pin_0
  N11: U4.Pin_2, IC8.GND, J1.pin1
  N12: U4.Pin_4, Part1.D1, R26.Pin_1
  N13: U4.Pin_5, R12.Pin_1
  N14: U2.Pin_1, R22.Pin_0
  N15: U2.Pin_2, IC6.GND, J3.pin1
  N16: U2.Pin_4, Part1.D5, R30.Pin_1
  N17: U5.Pin_1, R18.Pin_0
  N18: U5.Pin_2, IC2.GND, J7.pin1
  N19: U5.Pin_4, Part1.D4, R29.Pin_1
  N20: U5.Pin_5, R15.Pin_1
  N21: U6.Pin_1, R20.Pin_0
  N22: U6.Pin_2, IC4.GND, J5.pin1
  N23: U6.Pin_4, Part1.D0, R25.Pin_1
  N24: U6.Pin_5, R16.Pin_1
  N25: U7.Pin_1, R19.Pin_0
  N26: U7.Pin_2, IC3.GND, J6.pin1
  N27: U7.Pin_4, Part1.D2, R27.Pin_1
  N28: U7.Pin_5, R14.Pin_1
  N29: U8.Pin_1, R17.Pin_0
  N30: U8.Pin_2, IC1.GND, J8.pin1
  N31: U8.Pin_4, Part1.D6, R31.Pin_1
  N32: U8.Pin_5, R13.Pin_1
  N33: IC1.IN, J8.pin2
  N34: IC1.OUT, R17.Pin_1
  N35: IC2.IN, J7.pin2
  N36: IC2.OUT, R18.Pin_1
  N37: IC3.IN, J6.pin2
  N38: IC3.OUT, R19.Pin_1
  N39: IC4.IN, J5.pin2
  N40: IC4.OUT, R20.Pin_1
  N41: IC5.IN, J4.pin2
  N42: IC5.OUT, R21.Pin_1
  N43: IC6.IN, J3.pin2
  N44: IC6.OUT, R22.Pin_1
  N45: IC7.IN, J2.pin2
  N46: IC7.OUT, R23.Pin_1
  N47: IC8.IN, J1.pin2
  N48: IC8.OUT, R24.Pin_1
  GND: Part1.GND, R25.Pin_0, R26.Pin_0, R27.Pin_0, R28.Pin_0, R29.Pin_0, R30.Pin_0, R31.Pin_0, R32.Pin_0, BAT2.-
  N49: Part1.VBAT, BAT2.+
