# Fritzing sketch id185_Steuerplatine_0 (saved by Fritzing 0.8.7b)
circuit board: 6.9215cm x 5.33756cm
breadboards: 1

parts:
  U1 = PCF8574 [package="DIP16 [THT]"]
  U2 = PCF8574 [package="DIP16 [THT]"]
  Q2 = LTR-301 [package=ltr-301]
  IR1 = TSOP312.., 314.. [package=THT]
  1_0k = Resistor [tolerance=±1% resistance=1k package=THT]
  4_7k = Resistor [tolerance=±1% resistance=4.7k package=THT]
  4_7k_2 = Resistor [tolerance=±1% resistance=4.7k package=THT]
  Bauteil1 = Arduino Uno (Rev3)
  JP4 = M16 [package=1x16_machine-pin-header_lock.004]
  Temp = LM35 Temperature Sensor [package="TO92 [THT]"]
  LCD1 = LCD screen
  R1 = Rotary Potentiometer (Small) [maximum_resistance=100kΩ package=THT]

nets:
  GND: U1.A0, U1.A1, U1.A3, U1.GND, U2.A1, U2.A3, U2.GND, IR1.GND, 1_0k.Pin_0, Bauteil1.GND, Temp.GND, LCD1.VSS, R1.leg2
  N1: U1.P0, JP4.1
  N2: U1.P1, JP4.2
  N3: U1.P2, JP4.3
  N4: U1.P3, JP4.4
  N5: U1.P4, JP4.5
  N6: U1.P5, JP4.6
  N7: U1.P6, JP4.7
  N8: U1.P7, JP4.8
  N9: U1.SCL, U2.SCL, 4_7k_2.Pin_0, Bauteil1.A5/SCL
  N10: U1.SDA, U2.SDA, 4_7k.Pin_0, Bauteil1.A4/SDA
  5V: U1.VCC, U2.A0, U2.VCC, Q2.C, IR1.Vs, 4_7k.Pin_1, 4_7k_2.Pin_1, Bauteil1.5V, Temp.+Vs, LCD1.VDD, LCD1.LED+
  N11: U2.P0, JP4.9, LCD1.DB4
  N12: U2.P1, JP4.10, LCD1.DB5
  N13: U2.P2, JP4.11, LCD1.DB6
  N14: U2.P3, JP4.12, LCD1.DB7
  N15: U2.P4, JP4.13, LCD1.E
  N16: U2.P5, JP4.14, LCD1.R/W
  N17: U2.P6, JP4.15, LCD1.RS
  N18: U2.P7, JP4.16, LCD1.LED-
  Lightsensor: Q2.E, 1_0k.Pin_1, Bauteil1.A0
  IRSensor: IR1.Data, Bauteil1.D11_PWM/MOSI
  Tempsensor: Bauteil1.A2, Temp.Vout
  N19: LCD1.V0, R1.leg1

notes:
  Heimautomatisierung, Steuermodule für die Steuerung der Relais, ___1.0
  Use pin 0 to 7 (from the pinheader) to controll a 8 channle relay modul
