# Fritzing sketch id1861_Garage_0 (saved by Fritzing 0.9.2b)

parts:
  Composant1 = Arduino Uno (Rev3)
  U1 = ESP8266_module [part_number=ESP8266]
  U2 = RELAY [package=relay-g5q]
  U3 = RELAY [package=relay-g5q]
  S4 = mag-door
  S5 = mag-door
  R1 = Resistor [tolerance=±5% resistance=220 package=THT]
  R2 = Resistor [tolerance=±5% resistance=220 package=THT]

nets:
  N1: Composant1.D8, U2.COIL2
  N2: Composant1.D9_PWM, U2.COIL1
  N3: Composant1.D10_PWM/SS, U3.COIL2
  N4: Composant1.D11_PWM/MOSI, U3.COIL1
  N5: Composant1.GND, U1.connector6, R1.Pin_1, R2.Pin_1
  N6: Composant1.D0/RX, U1.connector7
  N7: Composant1.D1/TX, U1.connector0
  N8: Composant1.D3_PWM, S5.connector1, R2.Pin_0
  N9: Composant1.D5_PWM, S4.connector1, R1.Pin_0
  N10: Composant1.3V3, U1.connector1, U1.connector5
  N11: Composant1.5V, S4.connector0, S5.connector0
