# Fritzing sketch id1863_Autonomous_OGT_MK2_0 (saved by Fritzing 0.9.3b)

parts:
  Part1 = Arduino Mega 2560 (Rev3)
  Part2 = EasyDriver_v44
  Part6 = EasyDriver_v44
  M2 = Stepper Motor - Bipolar
  pH_Circuit1 = pH Circuit
  M1 = Stepper Motor - Bipolar
  Part7 = EasyDriver_v44
  Part8 = EasyDriver_v44
  M3 = Stepper Motor - Bipolar
  M4 = Stepper Motor - Bipolar
  Conductivity_Circuit1 = Conductivity Circuit

nets:
  N1: Part1.A14, Conductivity_Circuit1.PRB
  N2: Part1.A15, pH_Circuit1.PRB
  N3: Part1.D19/RX1, Part2.DIR
  N4: Part1.D18/TX1, Part2.STEP
  N5: Part1.D17_PWM/RX2, Part2.MS2
  N6: Part1.D16_PWM/TX2, Part2.ENABLE
  N7: Part1.D15/RX3, Part2.MS1
  N8: Part1.D14/TX3, Part6.DIR
  N9: Part1.D13_PWM, Part7.MS1
  N10: Part1.D12_PWM, Part7.ENABLE
  N11: Part1.D11_PWM, Part7.MS2
  N12: Part1.D10_PWM, Part7.STEP
  N13: Part1.D9_PWM, Part7.DIR
  N14: Part1.D8_PWM, Part8.MS1
  N15: Part1.D0_RX0, Part6.STEP
  N16: Part1.D1_TX0, Part6.MS2
  N17: Part1.D2_PWM, Part6.ENABLE
  N18: Part1.D3_PWM, Part6.MS1
  N19: Part1.D4_PWM, Part8.DIR
  N20: Part1.D5_PWM, Part8.STEP
  N21: Part1.D6_PWM, Part8.MS2
  N22: Part1.D7_PWM, Part8.ENABLE
  N23: Part1.D31, pH_Circuit1.Vcc
  N24: Part1.D33, Conductivity_Circuit1.Vcc
  GND: Part1.GND, Part2.GND, pH_Circuit1.GND, Conductivity_Circuit1.GND
  N25: Part2.OUT2A, M1.A
  N26: Part2.OUT2B, M1.C
  N27: Part2.OUT1A, M1.B
  N28: Part2.OUT1B, M1.D
  N29: Part6.OUT2A, M2.A
  N30: Part6.OUT2B, M2.C
  N31: Part6.OUT1A, M2.B
  N32: Part6.OUT1B, M2.D
  N33: Part7.OUT2A, M4.A
  N34: Part7.OUT2B, M4.C
  N35: Part7.OUT1A, M4.B
  N36: Part7.OUT1B, M4.D
  N37: Part8.OUT2A, M3.A
  N38: Part8.OUT2B, M3.C
  N39: Part8.OUT1A, M3.B
  N40: Part8.OUT1B, M3.D

notes:
  SMPP: pH Down
  SMPP: FloraBLOOM
