# Fritzing sketch id1864_GardenaDouble_0 (saved by Fritzing 0.9.3b)
circuit board: 4cm x 4cm
breadboards: 1

parts:
  IC3 = L293D [package=THT]
  L5 = Solenoid
  L6 = Solenoid
  R9 = Resistor [tolerance=±5% resistance=100 package=THT]
  R10 = Resistor [tolerance=±5% resistance=100 package=THT]
  R11 = Resistor [tolerance=±5% resistance=10 package=THT]
  R12 = Resistor [tolerance=±5% resistance=10 package=THT]
  D5 = Rectifier Diode [part_number=1N4001 package="300 mil [THT]"]
  D6 = Rectifier Diode [part_number=1N4001 package="300 mil [THT]"]
  Raspberry_Pi_1 = Raspberry Pi 3 [part_number=RPI-3-V1.2]
  VCC1 = Battery block 9V

nets:
  3V3: IC3.Enable_1, IC3.Enable_2, Raspberry_Pi_1.3v3, Raspberry_Pi_1.3V3
  N1: IC3.In_1, Raspberry_Pi_1.GPIO24
  N2: IC3.Out_1_(_Controlled_by_Enable_1_), R10.Pin_1, R12.Pin_1
  GND: IC3.0V, Raspberry_Pi_1.GND, VCC1.-
  N3: IC3.Out_2_(_Controlled_by_Enable_1_), L6.pin1
  N4: IC3.In_2, Raspberry_Pi_1.GPIO23
  N5: IC3.+Vmotor, IC3.+V, VCC1.+
  N6: IC3.In_3, Raspberry_Pi_1.GPIO17
  N7: IC3.Out_3_(_Controlled_by_Enable_2_), R9.Pin_1, R11.Pin_1
  N8: IC3.Out_4_(_Controlled_by_Enable_2_), L5.pin1
  N9: IC3.In_4, Raspberry_Pi_1.GPIO16
  N10: L5.pin2, R9.Pin_0, D5.cathode
  N11: L6.pin2, R10.Pin_0, D6.cathode
  N12: R11.Pin_0, D5.anode
  N13: R12.Pin_0, D6.anode

notes:
  Gardena C14e
  open
  close
  +
  gnd
  -
  9V
  V1
  V2
  Valve Control
  _______
  (M. Riedl '16)
