# Fritzing sketch id1865_Garduino_Concept_Made_by_BTC_0 (saved by Fritzing 0.9.3b)
breadboards: 1

parts:
  Part1 = Arduino Mega 2560 (Rev3)
  RHT1 = Humidity and Temperature Sensor RHT03
  R1 = Resistor [tolerance=±5% resistance=220 package=THT]
  Part2 = Soil Moisture Sensor
  M1 = DC Motor

nets:
  GND: Part1.GND, RHT1.GND_1, RHT1.GND_2, Part2.GND
  3V3: Part1.3V3, Part2.VCC
  5V: Part1.5V, RHT1.Vcc, M1.pin_1
  N1: Part1.D7_PWM, M1.pin_2
  N2: Part1.D28, Part2.SIG
  N3: RHT1.Data-signal, R1.Pin_0

notes:
  Output
  Input
  Garduino Example
