# Fritzing sketch id1866_Untitled_Sketch_3_0 (saved by Fritzing 0.9.3b)
breadboards: 1

parts:
  Part1 = Arduino Ethernet Shield (Rev3)
  Part2 = Arduino Uno (Rev3) - ICSP  # not connected
  U1 = GAS_SENSOR [package=mq-3]
  J1 = Piezo Speaker
  GSM_SIM_GPSR_SMS_SIM900_SIM1 = SIM800L [package=THT]

nets:
  N1: Part1.PWM_D9, GSM_SIM_GPSR_SMS_SIM900_SIM1.SIM_TXD
  N2: Part1.ETH_CS, GSM_SIM_GPSR_SMS_SIM900_SIM1.SIM_RXD
  GND: Part1.GND, U1.A1, J1.pin1, GSM_SIM_GPSR_SMS_SIM900_SIM1.GND
  N3: Part1.A0, U1.B1
  N4: Part1.PWM_D3, J1.pin2
  N5: U1.H1, U1.H2

notes:
  <--- Ethernet Shield
  <---Arduino UNO
  Use MQ2 sensor
  Stack the ethernet shield on the arduino board, then make the connections on the shield
  <---GSM Module
