# Fritzing sketch id1867_sensor_gas_0 (saved by Fritzing 0.9.2b)
circuit board: 8.46667cm x 5.64444cm
breadboards: 1

parts:
  U1 = SPARKCORE
  R1 = Resistor [tolerance=±5% resistance=4.7k package=THT]
  VCC1 = 4 x AAA Battery Mount
  J1 = Piezo Speaker
  U2 = GAS_SENSOR [package=mq-3]

nets (from the schematic view):
  N1: U1.connector43, R1.Pin_1, U2.B1
  N2: U1.connector55, J1.pin2
  N3: U1.connector61, R1.Pin_0, VCC1.-, J1.pin1, U2.H2
  N4: VCC1.+, U2.A1, U2.H1

notes:
  Black = Negative
  Red = Positive
