# Fritzing sketch id1868_GatoLaser_0 (saved by Fritzing 0.9.3b)
breadboards: 1

parts:
  Componente2 = Arduino Uno (Rev3)
  J1 = Basic Servo
  J2 = Basic Servo

nets:
  N1: Componente2.D5_PWM, J1.pulse
  N2: Componente2.D6_PWM, J2.pulse
  VCC: Componente2.5V, J1.vcc, J2.vcc
  GND: Componente2.GND, J1.gnd, J2.gnd

notes:
  Projeto:
  https://www.youtube.com/channel/UCmEgOeo6UQiMmfNwMCK8g8Q
