# Fritzing sketch id1869_GAUNTLIT.._CIRCUIT_0 (saved by Fritzing 0.9.0b)
breadboards: 1

parts:
  Part1 = USB LiPoly Charger
  U1 = LIPO-1000mAh [package=lipo-1000]
  LED1 = LED - 5mm [color="Red (633nm)" package="5 mm [THT]"]  # not connected
  C1 = Capacitor Polarized [package=panasonic_c]  # not connected

nets:
  N1: Part1.GND, U1.-
