# Fritzing sketch id186_8_LED_Board_DrexProjects_0 (saved by Fritzing 0.9.2b)
circuit board: 5.98592cm x 2.69652cm
breadboards: 1

parts:
  LED1 = LED - 3mm [color="Red (633nm)" package="3 mm [THT]"]
  R1 = Resistor [tolerance=±5% resistance=220 package=THT]
  LED2 = LED - 3mm [color="Red (633nm)" package="3 mm [THT]"]
  LED3 = LED - 3mm [color="Red (633nm)" package="3 mm [THT]"]
  R3 = Resistor [tolerance=±5% resistance=220 package=THT]
  LED4 = LED - 3mm [color="Red (633nm)" package="3 mm [THT]"]
  LED5 = LED - 3mm [color="Red (633nm)" package="3 mm [THT]"]
  LED6 = LED - 3mm [color="Red (633nm)" package="3 mm [THT]"]
  R2 = Resistor [tolerance=±5% resistance=220 package=THT]
  R6 = Resistor [tolerance=±5% resistance=220 package=THT]
  R5 = Resistor [tolerance=±5% resistance=220 package=THT]
  R4 = Resistor [tolerance=±5% resistance=220 package=THT]
  R7 = Resistor [tolerance=±5% resistance=220 package=THT]
  R8 = Resistor [tolerance=±5% resistance=220 package=THT]
  LED7 = LED - 3mm [color="Red (633nm)" package="3 mm [THT]"]
  LED8 = LED - 3mm [color="Red (633nm)" package="3 mm [THT]"]
  J8 = female pin header, 2 pins [form="♀ (female)"]
  J7 = female pin header, 2 pins [form="♀ (female)"]
  J3 = female pin header, 2 pins [form="♀ (female)"]
  J2 = female pin header, 2 pins [form="♀ (female)"]
  J6 = female pin header, 2 pins [form="♀ (female)"]
  J5 = female pin header, 2 pins [form="♀ (female)"]
  J4 = female pin header, 2 pins [form="♀ (female)"]
  5v = female pin header, 2 pins [form="♀ (female)"]
  J1 = female pin header, 2 pins [form="♀ (female)"]

nets:
  N1: LED1.cathode, LED2.cathode, LED3.cathode, LED4.cathode, LED5.cathode, LED6.cathode, LED7.cathode, LED8.cathode, 5v.pin1, 5v.pin2
  N2: LED1.anode, R1.Pin_1
  N3: R1.Pin_0, J1.pin1, J1.pin2
  N4: LED2.anode, R2.Pin_1
  N5: LED3.anode, R3.Pin_1
  N6: R3.Pin_0, J3.pin1, J3.pin2
  N7: LED4.anode, R4.Pin_1
  N8: LED5.anode, R5.Pin_1
  N9: LED6.anode, R6.Pin_1
  N10: R2.Pin_0, J2.pin1, J2.pin2
  N11: R6.Pin_0, J6.pin1, J6.pin2
  N12: R5.Pin_0, J5.pin1, J5.pin2
  N13: R4.Pin_0, J4.pin1, J4.pin2
  N14: R7.Pin_0, J7.pin1, J7.pin2
  N15: R7.Pin_1, LED7.anode
  N16: R8.Pin_0, J8.pin1, J8.pin2
  N17: R8.Pin_1, LED8.anode

notes:
  DrexProjects
  2016
