# Fritzing sketch id1871_gear_indicator_1.1_0 (saved by Fritzing 0.3.12b)
breadboards: 1

parts:
  DI1 = 7-Segment LED Display [package=THT]
  Arduino1 = Arduino
  R3 = Resistor [resistance=62 package=THT]
  LDR1 = Photocell (LDR) [package=THT]
  R9 = Resistor [resistance=1M package=THT]
  R4 = Resistor [resistance=62 package=THT]
  R2 = Resistor [resistance=62 package=THT]
  R1 = Resistor [resistance=62 package=THT]
  R6 = Resistor [resistance=62 package=THT]
  R7 = Resistor [resistance=62 package=THT]
  R8 = Resistor [resistance=62 package=THT]
  R5 = Resistor [resistance=150 package=THT]
  J1 = female pin header, 2 pins [form="♀ (female)"]

nets:
  N1: DI1.cathodeE, R8.Pin_0
  N2: DI1.cathodeD, R7.Pin_0
  GND: DI1.commAnode, Arduino1.GND, LDR1.pin_1, J1.pin2
  N3: DI1.cathodeC, R6.Pin_0
  N4: DI1.cathodeDP, R5.Pin_0
  N5: DI1.cathodeB, R4.Pin_1
  N6: DI1.cathodeA, R3.Pin_1
  N7: DI1.cathodeF, R2.Pin_1
  N8: DI1.cathodeG, R1.Pin_1
  N9: Arduino1.D9, R5.Pin_1
  N10: Arduino1.D8, R1.Pin_0
  N11: Arduino1.D7, R2.Pin_0
  N12: Arduino1.D6, R8.Pin_1
  N13: Arduino1.D5, R7.Pin_1
  N14: Arduino1.D4, R6.Pin_1
  N15: Arduino1.D3, R4.Pin_0
  N16: Arduino1.D2, R3.Pin_0
  5V: Arduino1.+5V, R9.Pin_0
  N17: Arduino1.A0, J1.pin1
  N18: Arduino1.A1, LDR1.pin_0, R9.Pin_1
