# Fritzing sketch id1872_Geekturnik2_0 (saved by Fritzing 0.9.2b)
breadboards: 1

parts:
  Часть1 = Arduino Nano (Rev3.0)
  U1 = ESP8266_module [part_number=ESP8266]
  Часть2 = SRF05 Ultrasonic Rangefinder
  Часть3 = rc522
  IC1 = SHIFT REGISTER [package=dil16]
  U2 = CAPSENSE_PAD [package=capsense_pad]  # not connected
  U3 = LCD-16X2 [package=lcd-16x2]
  LCM1602_IIC1 = generic_ic_dip_22_300mil.fzp [part_number="LCM1602 IIC" chip_label="LCM1602 IIC"]
  SG1 = Buzzer 12mm [package=buzzer-ccv-kit]
  LED2 = smd LED [color="Red (633nm)" package="0805 [SMD]"]  # not connected
  R3 = Resistor [tolerance=±5% resistance=220 package="0402 [SMD]"]
  R4 = Resistor [tolerance=±5% resistance=220 package="0402 [SMD]"]
  R5 = Resistor [tolerance=±5% resistance=220 package="0402 [SMD]"]
  R6 = Resistor [tolerance=±5% resistance=220 package="0402 [SMD]"]
  R7 = Resistor [tolerance=±5% resistance=220 package="0402 [SMD]"]
  LED3 = smd LED [color="Red (633nm)" package="0805 [SMD]"]  # not connected
  LED4 = smd LED [color="Red (633nm)" package="0805 [SMD]"]  # not connected
  LED5 = smd LED [color="Red (633nm)" package="0805 [SMD]"]  # not connected
  LED6 = smd LED [color="Red (633nm)" package="0805 [SMD]"]  # not connected
  U4 = CAPSENSE_PAD [package=capsense_pad]  # not connected

nets:
  N1: Часть1.GND, U1.connector6, Часть3.connector13
  N2: Часть1.D2, IC1.SER
  N3: Часть1.D3, IC1.RCK
  N4: Часть1.D4, IC1.SCK
  N5: Часть1.D5, Часть2.connector10
  N6: Часть1.D6, Часть2.connector9
  N7: Часть1.D7, U1.connector0
  N8: Часть1.D8, U1.connector7
  N9: Часть1.D9, Часть3.connector14
  N10: Часть1.D10, Часть3.connector8
  N11: Часть1.D11/MOSI, Часть3.connector10
  N12: Часть1.D12/MISO, Часть3.connector11
  N13: Часть1.A5, LCM1602_IIC1.connector19
  N14: Часть1.A4, LCM1602_IIC1.connector18
  N15: Часть1.3V3, U1.connector5, Часть3.connector15
  N16: Часть2.connector8, IC1.VCC, LCM1602_IIC1.connector17
  N17: Часть2.connector11, IC1.GND, IC1.G, LCM1602_IIC1.connector16, SG1.2
  N18: IC1.QC, SG1.1
  N19: IC1.QD, R3.Pin_0
  N20: IC1.QE, R4.Pin_0
  N21: IC1.QF, R5.Pin_0
  N22: IC1.QG, R6.Pin_0
  N23: IC1.QH, R7.Pin_0
  N24: U3.VSS, LCM1602_IIC1.connector0
  N25: U3.VDD, LCM1602_IIC1.connector1
  N26: U3.VO, LCM1602_IIC1.connector2
  N27: U3.RS, LCM1602_IIC1.connector3
  N28: U3.R_W, LCM1602_IIC1.connector4
  N29: U3.E, LCM1602_IIC1.connector5
  N30: U3.DB0, LCM1602_IIC1.connector6
  N31: U3.DB1, LCM1602_IIC1.connector7
  N32: U3.DB2, LCM1602_IIC1.connector8
  N33: U3.DB3, LCM1602_IIC1.connector9
  N34: U3.DB4, LCM1602_IIC1.connector10
  N35: U3.DB5, LCM1602_IIC1.connector11
  N36: U3.DB6, LCM1602_IIC1.connector12
  N37: U3.DB7, LCM1602_IIC1.connector13
  N38: U3.A, LCM1602_IIC1.connector14
  N39: U3.K, LCM1602_IIC1.connector15
