# Fritzing sketch id1873_generator_shield_0 (saved by Fritzing 0.9.2b)
circuit board: 6.88566cm x 5.36311cm
breadboards: 1

parts:
  7 = LED - 3mm [color="Red (633nm)" package="3 mm [THT]"]
  6 = LED - 3mm [color="Red (633nm)" package="3 mm [THT]"]
  5 = LED - 3mm [color="Red (633nm)" package="3 mm [THT]"]
  4 = LED - 3mm [color="Red (633nm)" package="3 mm [THT]"]
  3 = LED - 3mm [color="Red (633nm)" package="3 mm [THT]"]
  2 = LED - 3mm [color="Red (633nm)" package="3 mm [THT]"]
  1 = LED - 3mm [color="Red (633nm)" package="3 mm [THT]"]
  Arduino = Arduino Uno (Rev3)
  shift-register = 74HC595 [package="DIP16 [THT]"]
  VIN = male pin header, 2 pins [form="♂ (male)"]
  v_reg = Voltage Regulator - 5V [package="TO220 [THT]"]
  R-VIN = Resistor [tolerance=±5% resistance=140 package=THT]
  C3 = Ceramic Capacitor [capacitance=100nF package="200 mil [THT, multilayer]"]
  USB-CHARGER = USB Connectors [package=usb-a-s-nosilk-female]
  PWR = male pin header, 2 pins [form="♂ (male)"]
  0 = LED - 3mm [color="Red (633nm)" package="3 mm [THT]"]
  D = Rectifier Diode [part_number=1N4001 package="300 mil [THT]"]
  C1 = Electrolytic Capacitor [capacitance=1µF package="100 mil [THT, electrolytic]"]
  R-GND = Resistor [tolerance=±5% resistance=100 package=THT]
  C2 = Electrolytic Capacitor [capacitance=1µF package="100 mil [THT, electrolytic]"]
  servo = male pin header, 3 pins [form="♂ (male)"]
  D1-5 = male pin header, 5 pins [form="♂ (male)"]
  D10-13 = male pin header, 4 pins [form="♂ (male)"]
  D7-8 = male pin header, 2 pins [form="♂ (male)"]
  R7 = Resistor [tolerance=±5% resistance=220 package="1206 [SMD]"]
  R6 = Resistor [tolerance=±5% resistance=220 package="1206 [SMD]"]
  R5 = Resistor [tolerance=±5% resistance=220 package="1206 [SMD]"]
  R3 = Resistor [tolerance=±5% resistance=220 package="1206 [SMD]"]
  R2 = Resistor [tolerance=±5% resistance=220 package="1206 [SMD]"]
  R1 = Resistor [tolerance=±5% resistance=220 package="1206 [SMD]"]
  R0 = Resistor [tolerance=±5% resistance=220 package="1206 [SMD]"]
  LiPo_Charger = Power Cell LiPo Charger/Booster
  Pad1 = Pad [width=2 height=2 connect=center]
  Pad2 = Pad [width=2 height=2 connect=center]
  R4 = Resistor [tolerance=±5% resistance=220 package="1206 [SMD]"]
  S1 = Toggle Switch [package=THT]
  VBATT = female pin header, 2 pins [form="♀ (female)"]
  VCC_GND_ALT = female pin header, 3 pins [form="♀ (female)"]
  SDA_SCL_QST = female pin header, 3 pins [form="♀ (female)"]
  D0-1 = male pin header, 2 pins [form="♂ (male)"]
  OLED = female pin header, 4 pins [form="♀ (female)"]
  GND = female pin header, 1 pin [form="♀ (female)"]
  5V = female pin header, 1 pin [form="♀ (female)"]

nets:
  GND: 7.cathode, 6.cathode, 5.cathode, 4.cathode, 3.cathode, 2.cathode, 1.cathode, Arduino.GND, shift-register.GND, VIN.pin1, v_reg.GND, C3.0, USB-CHARGER.GND, 0.cathode, C1.-, R-GND.Pin_0, C2.-, servo.pin1, LiPo_Charger.GND, S1.L1, VBATT.pin2, VCC_GND_ALT.pin2, SDA_SCL_QST.pin3, OLED.pin1, GND.pin1
  N1: 7.anode, R7.Pin_1
  N2: 6.anode, R6.Pin_1
  N3: 5.anode, R5.Pin_1
  N4: 4.anode, R4.Pin_1
  N5: 3.anode, R3.Pin_1
  N6: 2.anode, R2.Pin_1
  N7: 1.anode, R1.Pin_1
  N8: Arduino.A0, R-VIN.Pin_0, R-GND.Pin_1
  N9: Arduino.A1, D1-5.pin1
  N10: Arduino.A2, D1-5.pin2
  N11: Arduino.A3, D1-5.pin3
  SDA: Arduino.A4/SDA, D1-5.pin4, SDA_SCL_QST.pin1, OLED.pin4
  SCL: Arduino.A5/SCL, D1-5.pin5, SDA_SCL_QST.pin2, OLED.pin3
  N12: Arduino.D8, D7-8.pin1
  D9: Arduino.D9_PWM, servo.pin3
  N13: Arduino.D10_PWM/SS, D10-13.pin4
  N14: Arduino.D11_PWM/MOSI, D10-13.pin3
  N15: Arduino.D12/MISO, D10-13.pin2
  N16: Arduino.D13/SCK, D10-13.pin1
  N17: Arduino.D0/RX, D0-1.pin2
  N18: Arduino.D1/TX, D0-1.pin1
  D2: Arduino.D2, VCC_GND_ALT.pin3
  D3: Arduino.D3_PWM, shift-register.OE
  N19: Arduino.D4, shift-register.DS
  N20: Arduino.D5_PWM, shift-register.ST_CP
  N21: Arduino.D6_PWM, shift-register.SH_CP
  N22: Arduino.D7, D7-8.pin2
  VCC2: Arduino.5V, shift-register.MR, shift-register.VCC, PWR.pin1, servo.pin2
  N23: shift-register.Q1, R1.Pin_0
  N24: shift-register.Q2, R2.Pin_0
  N25: shift-register.Q3, R3.Pin_0
  N26: shift-register.Q4, R4.Pin_0
  N27: shift-register.Q5, R5.Pin_0
  N28: shift-register.Q6, R6.Pin_0
  N29: shift-register.Q7, R7.Pin_0
  N30: shift-register.Q0, R0.Pin_0
  N31: VIN.pin2, D.anode
  N32: v_reg.input_voltage, R-VIN.Pin_1, D.cathode, C1.+
  5VIN: v_reg.output_voltage, C3.1, C2.+, LiPo_Charger.5VIN, Pad1.pad
  VCC: USB-CHARGER.VBUS, PWR.pin2, LiPo_Charger.VCC, Pad2.pad, VCC_GND_ALT.pin1, OLED.pin2, 5V.pin1
  N33: 0.anode, R0.Pin_1
  N34: LiPo_Charger.VBATT, VBATT.pin1
  N35: LiPo_Charger.EN, S1.COM

notes:
  - + S
  - +
  srData
  srLatch
  srClock
  4
  ~5
  ~6
  remove blob if lipo
  charger is connected
  ~3
  2
  1
  0
  7
  8
  S ~9
  ~10
  ~11
  12
  13
  A1-5
  A0 VOLT
  <220-1K
  on/off
  LiPo Fuel Gauge
  VCC GND ALT
  SDA SCL QST
  + -
  GND VDD SCK SDA
  srOE
  LFG-ALT
  sparkfun.com/products/10617
  LiPo Charger
  sparkfun.com/products/11231
  LiPo Fuel Gauge: D2,SDA,SCL
  shift-register:D3,D4,D5,D6
  D3: OE, active low (set low or use PWM)
  Generator Shield, Generator Shield for Arduino
  Generator Shield
  github.com/sondreolav/Generator-Shield
