# Fritzing sketch id1874_Untitled_Sketch_2_0 (saved by Fritzing 0.9.3b)

parts:
  Part1 = Arduino Nano (Rev3.0)
  U1 = ADXL335 [package=lfcsp-16]
  Motor2 = DC Motor
  IC1 = L293D [package=THT]
  Motor1 = DC Motor
  Electromagnet = Solenoid
  12V_battery = BC9VPC [package=bc9vpc]
  Switch = Momentary Switch [package=ksa_sealed_tac_switch]

nets:
  N1: Part1.GND, IC1.0V, Electromagnet.pin1, 12V_battery.V-
  N2: Part1.D10, IC1.In_2
  N3: Part1.D11/MOSI, IC1.In_1
  N4: Part1.D12/MISO, IC1.In_4
  N5: Part1.5V, IC1.Enable_1, IC1.Enable_2, IC1.+V
  N6: Part1.A4, U1.COM
  N7: Part1.A3, U1.ST
  N8: Part1.A2, U1.ZOUT
  N9: Part1.A1, U1.YOUT
  N10: Part1.A0, U1.XOUT
  N11: Part1.3V3, U1.VS
  N12: Part1.D13/SCK, IC1.In_3
  N13: Motor2.pin_1, IC1.Out_4_(_Controlled_by_Enable_2_)
  N14: Motor2.pin_2, IC1.Out_3_(_Controlled_by_Enable_2_)
  N15: IC1.Out_1_(_Controlled_by_Enable_1_), Motor1.pin_1
  N16: IC1.Out_2_(_Controlled_by_Enable_1_), Motor1.pin_2
  N17: IC1.+Vmotor, 12V_battery.V+, Switch.1
  N18: Electromagnet.pin2, Switch.4
