# Fritzing sketch id1875_schematic_0 (saved by Fritzing 0.9.3b)
breadboards: 1

parts:
  Part1 = Arduino Mega 2560 (Rev3)
  Part2 = Bluetooth HC-05 Macho
  Grove1 = Grove OLED 128x96
  Part3 = InvenSense MPU6050
  S2 = Pushbutton [package=THT]
  S3 = Pushbutton [package=THT]

nets:
  N1: Part1.D21/SCL, Grove1.SCL, Part3.SCL
  N2: Part1.D20/SDA, Grove1.SDA, Part3.SDA
  N3: Part1.D19/RX1, Part2.RXD
  N4: Part1.D18/TX1, Part2.TXD
  N5: Part1.D17_PWM/RX2, S2.leg0
  N6: Part1.D16_PWM/TX2, S3.leg0
  GND: Part1.GND, Part2.GND, Grove1.GND, Part3.GND, S2.leg1, S3.leg1
  VCC: Part1.5V, Part2.VCC, Grove1.VCC, Part3.VCC
