# Fritzing sketch id1876_Schaltplan_0 (saved by Fritzing 0.9.3b)
circuit board: 8.46667cm x 5.64444cm
breadboards: 1

parts:
  Bauteil1 = Arduino Micro (Rev3)
  LED3 = RGB LED (com. cathode, rgb) [package="5 mm [THT]"]
  LED4 = RGB LED (com. cathode, rgb) [package="5 mm [THT]"]
  RE1 = Rotary Encoder [package=THT]
  R4 = Resistor [tolerance=±5% resistance=220 package=THT]
  R5 = Resistor [tolerance=±5% resistance=220 package=THT]
  R6 = Resistor [tolerance=±5% resistance=220 package=THT]
  R7 = Resistor [tolerance=±5% resistance=220 package=THT]
  R9 = Resistor [tolerance=±5% resistance=220 package=THT]
  R10 = Resistor [tolerance=±5% resistance=220 package=THT]
  R11 = Resistor [tolerance=±5% resistance=220 package=THT]
  R12 = Resistor [tolerance=±5% resistance=220 package=THT]
  LED5 = RGB LED (com. cathode, rgb) [package="5 mm [THT]"]
  R13 = Resistor [tolerance=±5% resistance=220 package=THT]
  S1 = Tilt Switch [package=THT]
  R14 = Resistor [tolerance=±5% resistance=220 package=THT]
  LED6 = RGB LED (com. cathode, rgb) [package="5 mm [THT]"]
  R15 = Resistor [tolerance=±5% resistance=220 package=THT]
  R16 = Resistor [tolerance=±5% resistance=220 package=THT]
  R17 = Resistor [tolerance=±5% resistance=220 package=THT]

nets:
  N1: Bauteil1.D4_PWM/A6, R6.Pin_1
  N2: Bauteil1.D5_PWM, R5.Pin_1
  N3: Bauteil1.D6_PWM/A7, R4.Pin_1
  N4: Bauteil1.D7, R7.Pin_1
  N5: Bauteil1.D8_PWM/A8, R12.Pin_1
  N6: Bauteil1.D9_PWM/A9, R11.Pin_1
  N7: Bauteil1.D10_PWM/A10, R10.Pin_1
  N8: Bauteil1.D11_PWM, R9.Pin_1
  N9: Bauteil1.D12_PWM/A11, R13.Pin_1
  N10: Bauteil1.GND, S1.Pin_1
  N11: Bauteil1.A5, R17.Pin_1
  N12: Bauteil1.A4, R16.Pin_1
  N13: Bauteil1.A3, R15.Pin_1
  N14: Bauteil1.A2, RE1.EncoderPinA
  N15: Bauteil1.A1, RE1.EncoderPinB
  N16: LED3.red_anode, R10.Pin_0
  N17: LED3.common_cathode, LED4.common_cathode, RE1.EncoderPinC, LED5.common_cathode, R14.Pin_0, LED6.common_cathode
  N18: LED3.green_anode, R9.Pin_0
  N19: LED3.blue_anode, R13.Pin_0
  N20: LED4.red_anode, R6.Pin_0
  N21: LED4.green_anode, R5.Pin_0
  N22: LED4.blue_anode, R4.Pin_0
  N23: R7.Pin_0, LED5.red_anode
  N24: R11.Pin_0, LED5.blue_anode
  N25: R12.Pin_0, LED5.green_anode
  N26: S1.Pin_2, R14.Pin_1
  N27: LED6.red_anode, R15.Pin_0
  N28: LED6.green_anode, R16.Pin_0
  N29: LED6.blue_anode, R17.Pin_0
