# Fritzing sketch id1878_seguidor_de_luz_girasol_0 (saved by Fritzing 0.9.3b)
circuit board: 10.8043cm x 6.34804cm
breadboards: 1

parts:
  Componente1 = Arduino Uno (Rev3)
  R1 = Resistor [tolerance=±5% resistance=1k package=THT]
  R2 = Resistor [tolerance=±5% resistance=1k package=THT]
  J1 = Basic Servo
  R3 = PHOTOCELL [package=photocell-kit]
  R4 = PHOTOCELL [package=photocell-kit]

nets:
  N1: Componente1.A0, R2.Pin_0, R3.P$2
  N2: Componente1.A1, R1.Pin_0, R4.P$2
  N3: Componente1.D9_PWM, J1.pulse
  GND: Componente1.GND, R1.Pin_1, R2.Pin_1, J1.gnd
  5V: Componente1.5V, J1.vcc, R3.P$1, R4.P$1
