# Fritzing sketch id187_8_LED_Hookup_0 (saved by Fritzing 0.7.10b)
breadboards: 1

parts:
  Arduino1 = Arduino
  LED3 = red smd LED [package="1206 [SMD]"]
  LED8 = red smd LED [package="1206 [SMD]"]
  R1 = Resistor [tolerance=±5% resistance=10 package=THT]
  R2 = Resistor [tolerance=±5% resistance=10 package=THT]
  R3 = Resistor [tolerance=±5% resistance=10 package=THT]
  R4 = Resistor [tolerance=±5% resistance=10 package=THT]
  R5 = Resistor [tolerance=±5% resistance=10 package=THT]
  R6 = Resistor [tolerance=±5% resistance=10 package=THT]
  R7 = Resistor [tolerance=±5% resistance=10 package=THT]
  R8 = Resistor [tolerance=±5% resistance=10 package=THT]
  LED1 = white smd LED [package="1206 [SMD]"]
  LED2 = green smd LED [package="1206 [SMD]"]
  LED4 = Blue smd LED [package="1206 [SMD]"]
  LED5 = yellow smd LED [package="1206 [SMD]"]
  LED6 = white smd LED [package="1206 [SMD]"]
  LED7 = green smd LED [package="1206 [SMD]"]

nets:
  N1: Arduino1.GND, LED3.cathode, LED8.cathode, LED1.cathode, LED2.cathode, LED4.cathode, LED5.cathode, LED6.cathode, LED7.cathode
  N2: Arduino1.D13, R1.Pin_1
  N3: Arduino1.D12, R2.Pin_1
  N4: Arduino1.D11, R3.Pin_1
  N5: Arduino1.D10, R4.Pin_1
  N6: Arduino1.D7, R5.Pin_1
  N7: Arduino1.D6, R6.Pin_1
  N8: Arduino1.D5, R7.Pin_1
  N9: Arduino1.D4, R8.Pin_1
  N10: LED3.anode, R3.Pin_0
  N11: LED8.anode, R8.Pin_0
  N12: R1.Pin_0, LED1.anode
  N13: R2.Pin_0, LED2.anode
  N14: R4.Pin_0, LED4.anode
  N15: R5.Pin_0, LED5.anode
  N16: R6.Pin_0, LED6.anode
  N17: R7.Pin_0, LED7.anode

notes:
  8 LEDS
