# Fritzing sketch id1880_V1_Routing_Gizmo_0 (saved by Fritzing 0.9.1b)
breadboards: 1

parts:
  Part1 = Arduino Uno (Rev3)
  U1 = RELAY [package=relay-jzc]  # not connected
  U2 = RELAY [package=relay-jzc]  # not connected
  U3 = RELAY [package=relay-jzc]  # not connected
  U4 = RELAY [package=relay-jzc]  # not connected
  U5 = RELAY [package=relay-jzc]  # not connected
  U6 = RELAY [package=relay-jzc]  # not connected
  U7 = MLX90614 [package=to-39]
  VCC1 = Battery  # not connected
  VCC2 = Battery
  L1 = Solenoid  # not connected
  L2 = Solenoid  # not connected
  L3 = Solenoid  # not connected
  L4 = Solenoid  # not connected
  L5 = Solenoid  # not connected
  L6 = Solenoid  # not connected
  Power_plug1 = Power plug  # not connected
  D1 = Rectifier Diode [part_number=1N4001 package="Melf DO-213 AB [SMD]"]  # not connected
  D2 = Rectifier Diode [part_number=1N4001 package="Melf DO-213 AB [SMD]"]  # not connected
  D3 = Rectifier Diode [part_number=1N4001 package="Melf DO-213 AB [SMD]"]  # not connected
  D4 = Rectifier Diode [part_number=1N4001 package="Melf DO-213 AB [SMD]"]  # not connected
  D5 = Rectifier Diode [part_number=1N4001 package="Melf DO-213 AB [SMD]"]  # not connected
  D6 = Rectifier Diode [part_number=1N4001 package="Melf DO-213 AB [SMD]"]  # not connected

nets:
  N1: Part1.D9_PWM, U7.VSS
  N2: U7.SCL_VZ, VCC2.-
  N3: U7.PWM_SDA, VCC2.+

notes:
  12V wall transformer
  5V wall transformer
  PIR
  JD VCC + GND
  1     2          3   4   5   6
  8 RELAY MODULE
  VCC
