# Fritzing sketch id1881_Glitchduino_1_0_0 (saved by Fritzing 0.9.3b)
circuit board: 9.92398cm x 5.35018cm
breadboards: 2

parts:
  R1 = Photocell (LDR) [package=THT]
  J1 = female pin header, 2 pins [form="♀ (female)"]
  R2 = Photocell (LDR) [package=THT]
  J3 = female pin header, 2 pins [form="♀ (female)"]
  R4 = Photocell (LDR) [package=THT]
  R5 = Photocell (LDR) [package=THT]
  J5 = female pin header, 2 pins [form="♀ (female)"]
  R6 = Photocell (LDR) [package=THT]
  J6 = female pin header, 2 pins [form="♀ (female)"]
  R7 = Photocell (LDR) [package=THT]
  J7 = female pin header, 2 pins [form="♀ (female)"]
  R8 = Photocell (LDR) [package=THT]
  J8 = female pin header, 2 pins [form="♀ (female)"]
  R9 = Photocell (LDR) [package=THT]
  J9 = female pin header, 2 pins [form="♀ (female)"]
  R10 = Photocell (LDR) [package=THT]
  J10 = female pin header, 2 pins [form="♀ (female)"]
  6N138 = IC, DIP package, 8 pins [chip_label=6N138]
  D1 = Rectifier Diode [part_number=1N4148 package="300 mil [THT]"]
  220Ω = Resistor [tolerance=±5% resistance=220 package=THT]
  10kΩ = Resistor [tolerance=±5% resistance=10k package=THT]
  J2 = female pin header, 2 pins [form="♀ (female)"]
  470Ω = Resistor [tolerance=±5% resistance=470 package=THT]
  R3 = Photocell (LDR) [package=THT]
  J4 = female pin header, 2 pins [form="♀ (female)"]
  Bauteil1 = Arduino Mega 2560 (Rev3)
  R14 = Resistor [tolerance=±5% resistance=220 package=THT]
  R15 = Resistor [tolerance=±5% resistance=220 package=THT]
  R16 = Resistor [tolerance=±5% resistance=220 package=THT]
  R17 = Resistor [tolerance=±5% resistance=220 package=THT]
  R18 = Resistor [tolerance=±5% resistance=220 package=THT]
  R19 = Resistor [tolerance=±5% resistance=220 package=THT]
  R20 = Resistor [tolerance=±5% resistance=220 package=THT]
  R21 = Resistor [tolerance=±5% resistance=220 package=THT]
  R22 = Resistor [tolerance=±5% resistance=220 package=THT]
  R23 = Resistor [tolerance=±5% resistance=220 package=THT]
  LED2 = smd LED [color="Red (633nm)" package="1206 [SMD]"]
  LED3 = smd LED [color="Red (633nm)" package="1206 [SMD]"]
  LED4 = smd LED [color="Red (633nm)" package="1206 [SMD]"]
  LED5 = smd LED [color="Red (633nm)" package="1206 [SMD]"]
  LED6 = smd LED [color="Red (633nm)" package="1206 [SMD]"]
  LED7 = smd LED [color="Red (633nm)" package="1206 [SMD]"]
  LED8 = smd LED [color="Red (633nm)" package="1206 [SMD]"]
  LED9 = smd LED [color="Red (633nm)" package="1206 [SMD]"]
  LED10 = smd LED [color="Red (633nm)" package="1206 [SMD]"]
  LED11 = smd LED [color="Red (633nm)" package="1206 [SMD]"]
  DIN1 = DIN-5 jack (MIDI) [package=THT]

nets:
  N1: R1.pin_0, J1.pin1
  N2: R1.pin_1, J1.pin2
  N3: R2.pin_0, J2.pin1
  N4: R2.pin_1, J2.pin2
  N5: J3.pin1, R3.pin_0
  N6: J3.pin2, R3.pin_1
  N7: R4.pin_0, J4.pin1
  N8: R4.pin_1, J4.pin2
  N9: R5.pin_0, J5.pin1
  N10: R5.pin_1, J5.pin2
  N11: R6.pin_0, J6.pin1
  N12: R6.pin_1, J6.pin2
  N13: R7.pin_0, J7.pin1
  N14: R7.pin_1, J7.pin2
  N15: R8.pin_0, J8.pin1
  N16: R8.pin_1, J8.pin2
  N17: R9.pin_0, J9.pin1
  N18: R9.pin_1, J9.pin2
  N19: R10.pin_0, J10.pin1
  N20: R10.pin_1, J10.pin2
  N21: 6N138.pin2, D1.cathode, 220Ω.Pin_1
  N22: 6N138.pin3, DIN1.5
  N23: 6N138.pin4, D1.anode
  GND: 6N138.pin5, 10kΩ.Pin_1, Bauteil1.GND, LED2.cathode, LED3.cathode, LED4.cathode, LED5.cathode, LED6.cathode, LED7.cathode, LED8.cathode, LED9.cathode, LED10.cathode, LED11.cathode, DIN1.GND
  N24: 6N138.pin6, 470Ω.Pin_1, Bauteil1.D0_RX0
  N25: 6N138.pin7, 10kΩ.Pin_0
  N26: 6N138.pin8, 470Ω.Pin_0, Bauteil1.5V
  N27: 220Ω.Pin_0, DIN1.4
  N28: Bauteil1.D13_PWM, R21.Pin_0
  N29: Bauteil1.D10_PWM, R14.Pin_0
  N30: Bauteil1.D9_PWM, R23.Pin_0
  N31: Bauteil1.D8_PWM, R22.Pin_0
  N32: Bauteil1.D2_PWM, R19.Pin_1
  N33: Bauteil1.D3_PWM, R18.Pin_1
  N34: Bauteil1.D4_PWM, R17.Pin_1
  N35: Bauteil1.D5_PWM, R16.Pin_0
  N36: Bauteil1.D6_PWM, R15.Pin_0
  N37: Bauteil1.D7_PWM, R20.Pin_0
  N38: R14.Pin_1, LED11.anode
  N39: R15.Pin_1, LED2.anode
  N40: R16.Pin_1, LED3.anode
  N41: R17.Pin_0, LED4.anode
  N42: R18.Pin_0, LED6.anode
  N43: R19.Pin_0, LED7.anode
  N44: R20.Pin_1, LED8.anode
  N45: R21.Pin_1, LED5.anode
  N46: R22.Pin_1, LED9.anode
  N47: R23.Pin_1, LED10.anode

notes:
  220
  10k
  470
  6N138
  1N4148
  Choose your own LED. 1206 smd LEDs fit best. I chose bright white ones.
  Choose the right resistors for your LEDs.
