# Fritzing sketch id1882_mah_0 (saved by Fritzing 0.9.3b)
breadboards: 1

parts:
  Componente1 = Arduino Ethernet Shield (Rev3)
  R1 = Resistor [tolerance=±5% resistance=220 package="0603 [SMD]"]
  LED1 = smd LED [color="Red (633nm)" package="1206 [SMD]"]

nets:
  N1: Componente1.D2, R1.Pin_1
  N2: Componente1.GND, LED1.cathode
  N3: R1.Pin_0, LED1.anode
