# Fritzing sketch id1883_goduinoLogo_0 (saved by Fritzing 0.9.0b)
breadboards: 1

parts:
  part = Resistor [tolerance=±5% resistance=0 package=THT]
  part_2 = Ceramic Capacitor [capacitance=0pF package="100 mil [THT, multilayer]"]

nets:
  GND: part.Pin_0, part_2.0
