# Fritzing sketch id1885_FollowMe_Game1 (saved by Fritzing 0.5.2b)
breadboards: 1

parts:
  Arduino1 = Arduino
  LED1 = Blue LED - 5mm [package="5 mm [THT]"]
  J1 = Piezo Speaker
  LED1_2 = Red LED - 5mm [package="5 mm [THT]"]
  LED1_3 = green LED - 5mm [package="5 mm [THT]"]
  R1 = Resistor [resistance=220 package=THT]
  R1_2 = Resistor [resistance=220 package=THT]
  R1_3 = Resistor [resistance=220 package=THT]
  S1 = Pushbutton [package="[THT]"]
  S2 = Pushbutton [package="[THT]"]
  S3 = Pushbutton [package="[THT]"]
  R2 = Resistor [resistance=10k package=THT]
  R2_2 = Resistor [resistance=10k package=THT]
  R2_3 = Resistor [resistance=10k package=THT]

nets:
  N1: Arduino1.D9, J1.pin2
  N2: Arduino1.D7, S1.Pin_1, S1.Pin_2, R2_3.Pin_0
  N3: Arduino1.D6, LED1.anode
  N4: Arduino1.D5, S3.Pin_1, S3.Pin_2, R2.Pin_0
  N5: Arduino1.D4, LED1_3.anode
  N6: Arduino1.D3, S2.Pin_1, S2.Pin_2, R2_2.Pin_0
  N7: Arduino1.D2, LED1_2.anode
  N8: Arduino1.+5V, S1.Pin_3, S1.Pin_4, S2.Pin_3, S2.Pin_4, S3.Pin_3, S3.Pin_4
  N9: Arduino1.GND, J1.pin1, R1.Pin_1, R1_2.Pin_1, R1_3.Pin_1, R2.Pin_1, R2_2.Pin_1, R2_3.Pin_1
  N10: LED1.cathode, R1_3.Pin_0
  N11: LED1_2.cathode, R1_2.Pin_0
  N12: LED1_3.cathode, R1.Pin_0
