# Fritzing sketch id1886_analog_ir_sensor_0 (saved by Fritzing 0.9.3b)

parts:
  J2 = Infrared Proximity Sensor
  J3 = STM32 Nucleo boards

nets:
  N1: J2.Vout, J3.A5/SCL
  GND: J2.GND, J3.GND
  VCC: J2.Vcc, J3.5V
