# Fritzing sketch id1887_digital_ir_sensor_0 (saved by Fritzing 0.9.3b)

parts:
  Part3 = GP2Y0D810Z0F
  J1 = STM32 Nucleo boards

nets:
  N1: Part3.connector12, J1.5V
  N2: Part3.connector13, J1.D8
  N3: Part3.connector14, J1.GND
