# Fritzing sketch id1888_raspberry_L293D_DC_Motor_experiment_0 (saved by Fritzing 0.9.2b)
breadboards: 1

parts:
  Raspberry_Pi1 = Raspberry Pi B+
  IC1 = L293D [package=THT]
  BAT1 = BC9VPC [package=bc9vpc]
  M1 = DC Motor
  btn_1 = Pushbutton [package="[THT]"]
  btn_2 = Pushbutton [package="[THT]"]

nets:
  N1: Raspberry_Pi1.GPIO17, btn_1.Pin_3, btn_1.Pin_4
  N2: Raspberry_Pi1.GPIO27, btn_2.Pin_3, btn_2.Pin_4
  N3: Raspberry_Pi1.GND, IC1.0V, BAT1.V-, btn_1.Pin_1, btn_1.Pin_2, btn_2.Pin_1, btn_2.Pin_2
  N4: Raspberry_Pi1.GPIO23, IC1.In_3
  N5: Raspberry_Pi1.GPIO18, IC1.In_4
  N6: Raspberry_Pi1.5V, IC1.Enable_2, IC1.+V
  N7: IC1.+Vmotor, BAT1.V+
  N8: IC1.Out_3_(_Controlled_by_Enable_2_), M1.pin_2
  N9: IC1.Out_4_(_Controlled_by_Enable_2_), M1.pin_1

notes:
  import RPi.GPIO as GPIO
  import time
  from gpiozero import Motor, Button
  GPIO.setmode(GPIO.BCM)
  GPIO.setwarnings(False)
  motor = Motor(18, 23)
  btn_1 = Button(17)
  btn_2 = Button(27)
  try:
  while True:
  if btn_1.is_pressed :
  print('vooruit')
  motor.forward()
  elif btn_2.is_pressed :
  print('achteruit')
  motor.backward()
  else :
  print('wachten')
  motor.stop()
  except KeyboardInterrupt:
  print('EXIT')
  except:
  print('ERROR')
  finally:
  GPIO.cleanup()
