# Fritzing sketch id1889_GPO_Module_0 (saved by Fritzing 0.7.0b)
breadboards: 1

parts:
  74HC595 = IC, DIP package, 16 pins [chip_label=74HC595 spacing=300mil]
  LED1 = LED - 3mm [color="Blue (430nm)" package="3 mm [THT]"]
  LED2 = LED - 3mm [color="Blue (430nm)" package="3 mm [THT]"]
  LED3 = LED - 3mm [color="Blue (430nm)" package="3 mm [THT]"]
  LED4 = LED - 3mm [color="Blue (430nm)" package="3 mm [THT]"]
  LED5 = LED - 3mm [color="Blue (430nm)" package="3 mm [THT]"]
  LED6 = LED - 3mm [color="Blue (430nm)" package="3 mm [THT]"]
  LED7 = LED - 3mm [color="Blue (430nm)" package="3 mm [THT]"]
  LED8 = LED - 3mm [color="Blue (430nm)" package="3 mm [THT]"]
  R1 = Resistor [tolerance=±5% resistance=220 package=THT]
  R2 = Resistor [tolerance=±5% resistance=220 package=THT]
  R3 = Resistor [tolerance=±5% resistance=220 package=THT]
  R4 = Resistor [tolerance=±5% resistance=220 package=THT]
  R5 = Resistor [tolerance=±5% resistance=220 package=THT]
  R6 = Resistor [tolerance=±5% resistance=220 package=THT]
  R7 = Resistor [tolerance=±5% resistance=220 package=THT]
  R8 = Resistor [tolerance=±5% resistance=220 package=THT]
  C1 = Ceramic Capacitor [capacitance=1µF package="100 mil [THT, multilayer]"]
  IN = female pin header, 6 pins [form="♀ (female)"]
  OUT = female pin header, 6 pins [form="♀ (female)"]

nets:
  N1: 74HC595.pin1, R2.Pin_0
  N2: 74HC595.pin2, R3.Pin_0
  N3: 74HC595.pin3, R4.Pin_0
  N4: 74HC595.pin4, R5.Pin_0
  N5: 74HC595.pin5, R6.Pin_0
  N6: 74HC595.pin6, R7.Pin_0
  N7: 74HC595.pin7, R8.Pin_0
  N8: 74HC595.pin8, 74HC595.pin13, LED1.cathode, LED2.cathode, LED3.cathode, LED4.cathode, LED5.cathode, LED6.cathode, LED7.cathode, LED8.cathode, C1.0, IN.pin1, OUT.pin6
  N9: 74HC595.pin9, OUT.pin4
  N10: 74HC595.pin10, 74HC595.pin16, C1.1, IN.pin6, OUT.pin1
  N11: 74HC595.pin11, IN.pin5, OUT.pin2
  N12: 74HC595.pin12, IN.pin2, OUT.pin5
  N13: 74HC595.pin14, IN.pin3
  N14: 74HC595.pin15, R1.Pin_0
  N15: LED1.anode, R1.Pin_1
  N16: LED2.anode, R2.Pin_1
  N17: LED3.anode, R3.Pin_1
  N18: LED4.anode, R4.Pin_1
  N19: LED5.anode, R5.Pin_1
  N20: LED6.anode, R6.Pin_1
  N21: LED7.anode, R7.Pin_1
  N22: LED8.anode, R8.Pin_1

notes:
  StefansKits.eu
  GPO Breakout
