# Fritzing sketch id188_8_Sensor_1.2.1_0 (saved by Fritzing 0.9.0b)
circuit board: 11.4468cm x 4.34318cm
breadboards: 1

parts:
  LED1 = LED - 5mm [color="Infrared (940nm)" package="5 mm [THT]"]
  LED2 = LED - 5mm [color="Infrared (940nm)" package="5 mm [THT]"]
  LED3 = LED - 5mm [color="Infrared (940nm)" package="5 mm [THT]"]
  LED4 = LED - 5mm [color="Infrared (940nm)" package="5 mm [THT]"]
  LED5 = LED - 5mm [color="Infrared (940nm)" package="5 mm [THT]"]
  LED6 = LED - 5mm [color="Infrared (940nm)" package="5 mm [THT]"]
  LED7 = LED - 5mm [color="Infrared (940nm)" package="5 mm [THT]"]
  LED8 = LED - 5mm [color="Infrared (940nm)" package="5 mm [THT]"]
  DIO4 = LED - 5mm [color="Red (633nm)" package="5 mm [THT]"]
  DIO5 = LED - 5mm [color="Red (633nm)" package="5 mm [THT]"]
  DIO3 = LED - 5mm [color="Red (633nm)" package="5 mm [THT]"]
  DIO6 = LED - 5mm [color="Red (633nm)" package="5 mm [THT]"]
  DIO7 = LED - 5mm [color="Red (633nm)" package="5 mm [THT]"]
  DIO1 = LED - 5mm [color="Red (633nm)" package="5 mm [THT]"]
  DIO8 = LED - 5mm [color="Red (633nm)" package="5 mm [THT]"]
  DIO2 = LED - 5mm [color="Red (633nm)" package="5 mm [THT]"]
  R1 = Resistor [tolerance=±5% resistance=220 package=THT]
  R2 = Resistor [tolerance=±5% resistance=220 package=THT]
  R3 = Resistor [tolerance=±5% resistance=220 package=THT]
  R4 = Resistor [tolerance=±5% resistance=220 package=THT]
  R5 = Resistor [tolerance=±5% resistance=220 package=THT]
  R6 = Resistor [tolerance=±5% resistance=220 package=THT]
  R7 = Resistor [tolerance=±5% resistance=220 package=THT]
  R8 = Resistor [tolerance=±5% resistance=220 package=THT]
  LM324N2 = LM324N
  R9 = Resistor [tolerance=±5% resistance=220 package=THT]
  VCC = Battery
  R10 = Trimmer Potentiometer [maximum_resistance=10kΩ package=THT]
  LM324N1 = LM324N

nets:
  N1: LED1.cathode, LED2.cathode, LED3.cathode, LED4.cathode, LED5.cathode, LED6.cathode, LED7.cathode, LED8.cathode, R1.Pin_0, R2.Pin_0, R3.Pin_0, R4.Pin_0, R5.Pin_0, R6.Pin_0, R7.Pin_0, R8.Pin_0, LM324N2.connector10, VCC.-, R10.leg2, LM324N1.connector10
  N2: LED1.anode, LED2.anode, LED3.anode, LED4.anode, LED5.anode, LED6.anode, LED7.anode, LED8.anode, R9.Pin_0
  N3: DIO4.cathode, DIO5.cathode, DIO3.cathode, DIO6.cathode, DIO7.cathode, DIO1.cathode, DIO8.cathode, DIO2.cathode, LM324N2.connector3, R9.Pin_1, VCC.+, R10.leg1, LM324N1.connector3
  N4: DIO4.anode, R4.Pin_1, LM324N1.connector11
  N5: DIO5.anode, R5.Pin_1, LM324N2.connector9
  N6: DIO3.anode, R3.Pin_1, LM324N1.connector2
  N7: DIO6.anode, R6.Pin_1, LM324N2.connector4
  N8: DIO7.anode, R7.Pin_1, LM324N2.connector2
  N9: DIO1.anode, R1.Pin_1, LM324N1.connector9
  N10: DIO8.anode, R8.Pin_1, LM324N2.connector11
  N11: DIO2.anode, R2.Pin_1, LM324N1.connector4
  N12: LM324N2.connector1, LM324N2.connector5, LM324N2.connector8, LM324N2.connector12
  N13: LM324N1.connector1, LM324N1.connector5, LM324N1.connector8, LM324N1.connector12

notes:
  Sensor Array 1.2
  SUYASH
