# Fritzing sketch id1891_ARDUINO_Nano_GPS_PS2_MG210_0 (saved by Fritzing 0.9.3b)
circuit board: 5.64444cm x 8.46667cm
breadboards: 1

parts:
  ARDUINO_Nano = Arduino Nano (Rev3.0)
  GPS_HOLUX_MG-210_-_PS2 = mini DIN 6 Connector [package=mini-din6]
  Display1 = LCD-16X2 [package=lcd-16x2_noholes]
  S1 = Pushbutton [package="[SMD]"]
  S2 = Pushbutton [package="[SMD]"]
  S5 = Pushbutton [package="[SMD]"]
  S3 = Pushbutton [package="[SMD]"]
  S4 = Pushbutton [package="[SMD]"]
  Trimmer1 = Trimmer Potentiometer [maximum_resistance=10kΩ package=THT]
  1Wire = Header 3 [package=molex-1x3_lock]
  R3 = Resistor [tolerance=±5% resistance=10k package=THT]
  R1 = Resistor [tolerance=±5% resistance=10k package=THT]
  R4 = Resistor [tolerance=±5% resistance=10k package=THT]
  R5 = Resistor [tolerance=±5% resistance=10k package=THT]
  R2 = Resistor [tolerance=±5% resistance=10k package=THT]
  I2C = I2C Header

nets:
  N1: ARDUINO_Nano.D2, Display1.DB7
  N2: ARDUINO_Nano.D3, Display1.DB6
  N3: ARDUINO_Nano.D4, Display1.DB5
  N4: ARDUINO_Nano.D5, Display1.DB4
  N5: ARDUINO_Nano.D6, GPS_HOLUX_MG-210_-_PS2.5
  N6: ARDUINO_Nano.D7, GPS_HOLUX_MG-210_-_PS2.3
  N7: ARDUINO_Nano.D10, 1Wire.2
  N8: ARDUINO_Nano.D11/MOSI, Display1.E
  N9: ARDUINO_Nano.D12/MISO, Display1.RS
  5V: ARDUINO_Nano.5V, GPS_HOLUX_MG-210_-_PS2.2, Display1.VDD, Display1.A, S1.Pin_3, S1.Pin_4, S2.Pin_3, S2.Pin_4, S5.Pin_1, S5.Pin_2, S3.Pin_1, S3.Pin_2, S4.Pin_1, S4.Pin_2, Trimmer1.leg2, 1Wire.1, I2C.connector0
  N10: ARDUINO_Nano.A5, I2C.connector2
  N11: ARDUINO_Nano.A4, I2C.connector1
  N12: ARDUINO_Nano.A3, S1.Pin_1, S1.Pin_2, R1.Pin_1
  N13: ARDUINO_Nano.A2, S2.Pin_1, S2.Pin_2, R2.Pin_1
  N14: ARDUINO_Nano.A1, S3.Pin_3, S3.Pin_4, R3.Pin_1
  N15: ARDUINO_Nano.A0, S4.Pin_3, S4.Pin_4, R4.Pin_1
  N16: ARDUINO_Nano.D13/SCK, S5.Pin_3, S5.Pin_4, R5.Pin_1
  N17: GPS_HOLUX_MG-210_-_PS2.4, Display1.VSS, Display1.R_W, Display1.K, Trimmer1.leg1, 1Wire.3, R3.Pin_0, R1.Pin_0, R4.Pin_0, R5.Pin_0, R2.Pin_0, I2C.connector3
  N18: Display1.VO, Trimmer1.wiper
