# Fritzing sketch id1892_GPS_tracker_0 (saved by Fritzing 0.9.3b)
breadboards: 1

parts:
  Part1 = Arduino Uno (Rev3)
  LED1 = LED - 5mm [color="Green (555nm)" package="5 mm [THT]"]
  LED2 = LED - 5mm [color="Blue (505nm)" package="5 mm [THT]"]
  R2 = Resistor [tolerance=±5% resistance=220 package=THT]
  R3 = Resistor [tolerance=±5% resistance=220 package=THT]
  R4 = Resistor [tolerance=±5% resistance=10k package=THT]
  S2 = Momentary Switch [package=ksa_sealed_tac_switch]
  R5 = Resistor [tolerance=±5% resistance=10k package=THT]
  S3 = Momentary Switch [package=ksa_sealed_tac_switch]

nets:
  N1: Part1.D2, R5.Pin_0, S3.3
  N2: Part1.D3_PWM, R4.Pin_0, S2.3
  N3: Part1.D4, LED1.anode
  N4: Part1.D5_PWM, LED2.anode
  N5: Part1.5V, S2.1, S3.1
  N6: Part1.GND, R2.Pin_0, R3.Pin_0, R4.Pin_1, R5.Pin_1
  N7: LED1.cathode, R2.Pin_1
  N8: LED2.cathode, R3.Pin_1
