# Fritzing sketch id1893_brilloLED_potenciometro_DIMAS_0 (saved by Fritzing 0.7.5b)
breadboards: 1

parts:
  LED1 = LED - 5mm [color="Red (633nm)" package="5 mm [THT]"]
  R2 = Resistor [tolerance=±5% resistance=220 package=THT]
  Arduino1 = Arduino  # not connected
  R3 = Rotary Potentiometer (Small) [maximum_resistance=100kΩ]

nets:
  N1: LED1.cathode, R2.Pin_0
  N2: R2.Pin_1, R3.leg2
