# Fritzing sketch id1895_grbl_db_0 (saved by Fritzing 0.9.2b)
circuit board: 8.46667cm x 5.64444cm
breadboards: 2

parts:
  Part2 = DB25F
  S1 = Momentary Switch [package=ksa_sealed_tac_switch]
  S2 = Momentary Switch [package=ksa_sealed_tac_switch]
  S3 = Momentary Switch [package=ksa_sealed_tac_switch]
  S4 = Momentary Switch [package=ksa_sealed_tac_switch]
  R1 = Resistor [tolerance=±5% resistance=10k package=THT]
  R3 = Resistor [tolerance=±5% resistance=10k package=THT]
  R4 = Resistor [tolerance=±5% resistance=10k package=THT]
  R2 = Resistor [tolerance=±5% resistance=10k package=THT]
  Part1 = Arduino Uno (Rev3)
  Power = LED - 3mm [color="Red (633nm)" package="3 mm [THT]"]
  DIR = LED - 3mm [color="Green (565nm)" package="3 mm [THT]"]
  R5 = Resistor [tolerance=±5% resistance=680 package=THT]
  R6 = Resistor [tolerance=±5% resistance=680 package=THT]

nets:
  N1: Part2.pin1, Part1.D11_PWM/MOSI
  N2: Part2.pin2, Part1.D2
  N3: Part2.pin3, Part1.D4
  N4: Part2.pin4, Part1.D6_PWM
  N5: Part2.pin5, Part1.D3_PWM
  N6: Part2.pin6, Part1.D5_PWM
  N7: Part2.pin7, Part1.D7
  N8: Part2.pin11, Part1.D9_PWM
  N9: Part2.pin12, Part1.D10_PWM/SS
  N10: Part2.pin13, Part1.D12/MISO
  N11: Part2.pin18, Part2.pin19, Part2.pin20, Part2.pin21, Part2.pin22, Part2.pin23, Part2.pin24, Part2.pin25, S1.2, S2.2, S3.2, S4.2, Part1.GND, Power.anode, DIR.anode
  N12: S1.1, R1.Pin_0, Part1.A0
  N13: S2.1, R2.Pin_0, Part1.A1
  N14: S3.1, R3.Pin_0, Part1.A2
  N15: S4.1, R4.Pin_0
  N16: R1.Pin_1, R3.Pin_1, R4.Pin_1, R2.Pin_1, Part1.5V, R6.Pin_0
  N17: Part1.D13/SCK, R5.Pin_0
  N18: Power.cathode, R6.Pin_1
  N19: DIR.cathode, R5.Pin_1
