# Fritzing sketch id1897_finalgarden_1_0 (saved by Fritzing 0.9.2b)
circuit board: 6.88566cm x 5.36311cm
breadboards: 1

parts:
  LD1117VXX = V_REG_LD1117VXX [package=78xxl]
  Greenhouse_Shield = Arduino Uno (Rev3)
  DHT22 = Humidity and Temperature Sensor RHT03
  R1 = Resistor [tolerance=±5% resistance=10k package=THT]
  DS1307 = DS1307 [package=THT]
  BAT1 = Battery Holders [package=battcom_20mm_pth]
  Y1 = CRYSTAL [package=crystal-32khz-smd_epson_mc146]
  R2 = Resistor [tolerance=±5% resistance=10k package=THT]
  R3 = Resistor [tolerance=±5% resistance=10k package=THT]
  SoilTmp = screw terminal, 3 pins
  R4 = Resistor [tolerance=±5% resistance=4.7k package=THT]
  ESP8266-01 = ESP8266_module [part_number=ESP8266]
  UltraSonic = screw terminal, 4 pins
  Soil_Moisture = screw terminal, 4 pins
  Pump = screw terminal, 3 pins
  Heating = screw terminal, 3 pins

nets:
  N1: LD1117VXX.OUT, ESP8266-01.connector1, ESP8266-01.connector5
  GND: LD1117VXX.GND, Greenhouse_Shield.GND, DHT22.GND_2, R1.Pin_1, DS1307.0V, BAT1.-, SoilTmp.pin1, ESP8266-01.connector6, UltraSonic.pin1, Soil_Moisture.pin1, Pump.pin1, Heating.pin1
  5V: LD1117VXX.IN, Greenhouse_Shield.5V, DHT22.Vcc, DS1307.+V, R2.Pin_0, R3.Pin_0, SoilTmp.pin3, R4.Pin_1, UltraSonic.pin4, Soil_Moisture.pin2, Pump.pin3, Heating.pin3
  N2: Greenhouse_Shield.A0, Soil_Moisture.pin4
  N3: Greenhouse_Shield.A1, DS1307.Vbat_-_Backup_Supply, BAT1.+
  N4: Greenhouse_Shield.A4/SDA, DS1307.SDA_-_I2C_Data, R2.Pin_1
  N5: Greenhouse_Shield.A5/SCL, DS1307.SCL_-_I2C_Clock, R3.Pin_1
  N6: Greenhouse_Shield.D9_PWM, DHT22.Data-signal, R1.Pin_0
  N7: Greenhouse_Shield.D12/MISO, Heating.pin2
  N8: Greenhouse_Shield.D13/SCK, Pump.pin2
  N9: Greenhouse_Shield.D0/RX, ESP8266-01.connector0
  N10: Greenhouse_Shield.D1/TX, ESP8266-01.connector7
  N11: Greenhouse_Shield.D2, SoilTmp.pin2, R4.Pin_0
  N12: Greenhouse_Shield.D5_PWM, UltraSonic.pin3
  N13: Greenhouse_Shield.D6_PWM, UltraSonic.pin2
  N14: Greenhouse_Shield.D7, Soil_Moisture.pin3
  N15: DS1307.X1_-_Crystal, Y1.2
  N16: DS1307.X2_-_Crystal, Y1.1
