# Fritzing sketch id1899_level+shifter_0 (saved by Fritzing 0.8.7b)
circuit board: 4.49649cm x 3.6cm
breadboards: 1

parts:
  Q1 = MOSFET-NCHANNEL [package=to-92]
  Q2 = MOSFET-NCHANNEL [package=to-92]
  Q3 = MOSFET-NCHANNEL [package=to-92]
  Q4 = MOSFET-NCHANNEL [package=to-92]
  R1 = Resistor [tolerance=±5% resistance=10k package=THT]
  R3 = Resistor [tolerance=±5% resistance=10k package=THT]
  R4 = Resistor [tolerance=±5% resistance=10k package=THT]
  R2 = Resistor [tolerance=±5% resistance=10k package=THT]
  J1 = GROVE_VERTICAL_CONNECTOR_OK [form="♀ (female)"]
  J3 = GROVE_VERTICAL_CONNECTOR_OK [form="♀ (female)"]

nets:
  N1: Q1.D, Q2.D
  N2: Q1.S, R1.Pin_1, J1.connector0
  N3: Q1.G, Q3.G, R1.Pin_0, R3.Pin_0, J1.connector2
  N4: Q2.S, R2.Pin_0, J3.connector0
  N5: Q2.G, Q4.G, R4.Pin_1, R2.Pin_1, J3.connector2
  N6: Q3.D, Q4.D
  N7: Q3.S, R3.Pin_1, J1.connector1
  N8: Q4.S, R4.Pin_0, J3.connector1
  GND: J1.connector3, J3.connector3

notes:
  SDA
  SCL
  VCC 3V
  GND
  3.3V
  VCC 5V
