# Fritzing sketch id1900_Untitled_Sketch_0 (saved by Fritzing 0.9.3b)
breadboards: 1

parts:
  Part1 = Arduino Uno (Rev3)
  R1 = Resistor [tolerance=±5% resistance=220 package=THT]
  LED1 = LED - 5mm [color="Blue (505nm)" package="5 mm [THT]"]

nets:
  N1: Part1.D10_PWM/SS, R1.Pin_1
  N2: Part1.GND, LED1.cathode
  N3: R1.Pin_0, LED1.anode
