# Fritzing sketch id1901_Alarmanlage_0 (saved by Fritzing 0.7.5b)
breadboards: 1

parts:
  U1 = Voltage Regulator - 5V [package="TO220 [THT]"]
  U2 = atmega168 [package="DIP28 [THT]"]
  Power_plug1 = Power plug
  J5 = female pin header, 14 pins [form="♀ (female rounded)"]
  S2 = Pushbutton [package="[THT]"]
  C2 = Electrolytic Capacitor [capacitance=10µF rated_voltage=35V package="100 mil [THT, electrolytic]"]
  C1 = Electrolytic Capacitor [capacitance=10µF rated_voltage=35V package="100 mil [THT, electrolytic]"]
  C6 = Ceramic Capacitor [capacitance=22pF rated_voltage=35V package="200 mil [THT, multilayer]"]
  C5 = Ceramic Capacitor [capacitance=22pF rated_voltage=35V package="200 mil [THT, multilayer]"]
  XTAL1 = Crystal [frequency="16 Mhz" package=THT]
  R2 = Resistor [tolerance=±5% resistance=1k package=THT]
  J4 = female pin header, 14 pins [form="♀ (female rounded)"]
  J6 = Piezo Speaker  # not connected
  R3 = Resistor [tolerance=±5% resistance=220 package=THT]
  S3 = Round Pushbutton
  R4 = Resistor [tolerance=±5% resistance=220 package=THT]
  R5 = Resistor [tolerance=±5% resistance=220 package=THT]
  LED1 = LED - 5mm [color="Green (570nm)" package="5 mm [THT]"]
  LED2 = LED - 5mm [color="Red (633nm)" package="5 mm [THT]"]

nets:
  N1: U1.input_voltage, Power_plug1.VCC, C1.+
  GND: U1.GND, U2.Pin_8, U2.Pin_22, Power_plug1.GND, J5.pin8, S2.Pin_3, S2.Pin_4, C2.-, C1.-, C6.0, C5.1, J4.pin7, R3.Pin_1, LED1.cathode, LED2.cathode
  N2: U1.output_voltage, U2.Pin_7, U2.Pin_20, U2.Pin_21, J5.pin7, C2.+, R2.Pin_0, J4.pin8, J4.pin9, S3.leg1
  N3: U2.Pin_1, J5.pin1, S2.Pin_1, S2.Pin_2, R2.Pin_1
  N4: U2.Pin_2, J5.pin2
  N5: U2.Pin_3, J5.pin3
  N6: U2.Pin_4, J5.pin4
  N7: U2.Pin_5, J5.pin5
  N8: U2.Pin_6, J5.pin6
  N9: U2.Pin_9, J5.pin9, C6.1, XTAL1.pin_0
  N10: U2.Pin_10, J5.pin10, C5.0, XTAL1.pin_1
  N11: U2.Pin_11, J5.pin11
  N12: U2.Pin_12, J5.pin12
  N13: U2.Pin_13, J5.pin13
  N14: U2.Pin_14, J5.pin14
  N15: U2.Pin_15, J4.pin14, S3.leg0
  N16: U2.Pin_16, J4.pin13, R3.Pin_0
  N17: U2.Pin_17, J4.pin12
  N18: U2.Pin_18, J4.pin11, R4.Pin_1
  N19: U2.Pin_19, J4.pin10, R5.Pin_1
  N20: U2.Pin_23, J4.pin6
  N21: U2.Pin_24, J4.pin5
  N22: U2.Pin_25, J4.pin4
  N23: U2.Pin_26, J4.pin3
  N24: U2.Pin_27, J4.pin2
  N25: U2.Pin_28, J4.pin1
  N26: R4.Pin_0, LED1.anode
  N27: R5.Pin_0, LED2.anode

notes:
  TX -
  RX +
  Speaker
  TC35
  DYP-ME003 +
  -
  T
