# Fritzing sketch id1901_fors_senser (saved by Fritzing 0.3.14b)
breadboards: 1

parts:
  Arduino1 = Arduino
  LED2 = Red LED - 5mm
  LED3 = Red LED - 5mm
  LED4 = Red LED - 5mm
  LED5 = Red LED - 5mm
  LED6 = Red LED - 5mm  # not connected
  R2 = Resistor [resistance=1k package=THT]
  R3 = Resistor [resistance=1k package=THT]
  R4 = Resistor [resistance=1k package=THT]
  R5 = Resistor [resistance=1k package=THT]
  R6 = Resistor [resistance=1k package=THT]
  J1 = Basic Force Sensing Resistor (FSR) [package=THT]
  R7 = Resistor [resistance=220 package=THT]

nets:
  N1: Arduino1.GND, J1.pin_0
  N2: Arduino1.D13, R6.Pin_0
  N3: Arduino1.D12, R3.Pin_0
  N4: Arduino1.D11, R2.Pin_0, R4.Pin_0
  N5: Arduino1.D10, R5.Pin_0
  N6: Arduino1.A2, R7.Pin_1
  N7: LED2.anode, R6.Pin_1
  N8: LED3.anode, R3.Pin_1
  N9: LED4.anode, R2.Pin_1, R4.Pin_1
  N10: LED5.anode, R5.Pin_1
  N11: J1.pin_1, R7.Pin_0
