# Fritzing sketch id1903_ArduTrackv1.2_0 (saved by Fritzing 0.8.3b)

parts:
  Part1 = Arduino GSM Shield
  GPS1 = Adafruit_Ultimate_GPS_Breakout

nets:
  N1: Part1.PWM_D9, GPS1.connector6
  N2: Part1.D8, GPS1.connector5
  N3: Part1.5V, GPS1.connector8
  N4: Part1.AGND, GPS1.connector7
