# Fritzing sketch id1904_guardian_couch_monkey_0 (saved by Fritzing 0.7.0b)
breadboards: 1

parts:
  SPDT_5VDC_Relay_RadioShack_275-0240 = Componente_sem_nome
  Arduino_Duemilanove = Arduino
  VCC1 = Battery
  M1 = DC Motor
  PIR_Sensor = mystery part, 3 pins [chip_label=? spacing=300mil]
  part = mystery part, 3 pins [chip_label=? spacing=300mil]  # not connected
  part_2 = Resistor [tolerance=±5% resistance=220 package=THT]  # not connected

nets:
  N1: SPDT_5VDC_Relay_RadioShack_275-0240.connector0, Arduino_Duemilanove.GND, PIR_Sensor.pin2
  N2: SPDT_5VDC_Relay_RadioShack_275-0240.connector1, Arduino_Duemilanove.D13
  N3: SPDT_5VDC_Relay_RadioShack_275-0240.connector2, VCC1.-
  N4: SPDT_5VDC_Relay_RadioShack_275-0240.connector3, M1.pin_2
  N5: Arduino_Duemilanove.D12, PIR_Sensor.pin1
  N6: Arduino_Duemilanove.+5V, PIR_Sensor.pin3
  N7: VCC1.+, M1.pin_1
