# Fritzing sketch id1905_Guincho_Robotico___arduino_e_servomotor_0 (saved by Fritzing 0.7.12b)
breadboards: 1

parts:
  R1 = Rotary Potentiometer (Large) [maximum_resistance=100kΩ package=THT]
  R2 = Rotary Potentiometer (Large) [maximum_resistance=100kΩ package=THT]
  R3 = Rotary Potentiometer (Large) [maximum_resistance=100kΩ package=THT]
  Arduino1 = Arduino
  J1 = Basic Servo
  J2 = Basic Servo
  J3 = Basic Servo
  VCC1 = 4 x AAA Battery Mount

nets:
  N1: R1.leg1, R2.leg1, R3.leg1, Arduino1.+5V
  N2: R1.wiper, Arduino1.A0
  GND: R1.leg2, R2.leg2, R3.leg2, Arduino1.GND, J1.gnd, J2.gnd, J3.gnd, VCC1.-
  N3: R2.wiper, Arduino1.A1
  N4: R3.wiper, Arduino1.A2
  N5: Arduino1.D4, J3.pulse
  N6: Arduino1.D3, J2.pulse
  N7: Arduino1.D2, J1.pulse
