# Fritzing sketch id1906_ultrasound_wifi_0 (saved by Fritzing 0.9.2b)
breadboards: 1

parts:
  Part1 = Arduino Uno (Rev3)
  LED1 = LED - 5mm [color="Green (555nm)" package="5 mm [THT]"]
  R1 = Resistor [tolerance=±5% resistance=220 package=THT]
  Part2 = SRF05 Ultrasonic Rangefinder
  U1 = ESP8266_module [part_number=ESP8266]

nets:
  N1: Part1.D8, Part2.connector10
  N2: Part1.D9_PWM, Part2.connector9
  N3: Part1.D0/RX, U1.connector0
  N4: Part1.D1/TX, U1.connector7
  N5: Part1.D7, LED1.anode
  N6: Part1.3V3, U1.connector1, U1.connector5
  N7: Part1.5V, Part2.connector8
  N8: Part1.GND, Part2.connector11, U1.connector6
  N9: LED1.cathode, R1.Pin_0
