# Fritzing sketch id1907_Mini_Guitar_Amp___Rev5_0 (saved by Fritzing 0.9.2b)
circuit board: 4.5cm x 5.1cm
breadboards: 1

parts:
  +_SP1_- = SPEAKER [package=pcb_mount_speaker]
  C1 = Ceramic Capacitor [capacitance=0.01µF voltage=10V package="100 mil [THT, multilayer]"]
  R3 = Resistor [tolerance=±5% resistance=10 package=THT]
  C5 = Ceramic Capacitor [capacitance=47nF voltage=10V package="100 mil [THT, multilayer]"]
  C6 = Electrolytic Capacitor [capacitance=220µF voltage=10V package="100 mil [THT, electrolytic]"]
  C4 = Ceramic Capacitor [capacitance=33nF voltage=10V package="100 mil [THT, multilayer]"]
  C2 = Ceramic Capacitor [capacitance=100µF voltage=10V package="100 mil [THT, multilayer]"]
  C3 = Ceramic Capacitor [capacitance=10µF voltage=10V package="100 mil [THT, multilayer]"]
  U1 = LM386 [package=dip08]
  SW2 = SWITCH-SPST-2 [package=switch-spst-vertical]
  A_Out = AUDIO-JACK2 [package=audio-jack]
  R1 = Resistor [tolerance=±5% resistance=220 package=THT]
  R2 = Resistor [tolerance=±5% resistance=10k package=THT]
  LED1 = LED - 3mm [color="Red (633nm)" package="3 mm [THT]"]
  SW1 = SWITCH-SPST-2 [package=switch-spst-vertical]
  Trimpot = POT [package=alps_pot]
  +BAT9V- = Battery block 9V
  J1 = Power Jack [package=power_jack_pth_lock]
  D1 = Diode [package=diode-1n4148]
  A_In = AUDIO-JACK2 [package=audio-jack]

nets:
  N1: +_SP1_-.+, A_Out.RSH, A_Out.TSH
  GND: +_SP1_-.-, C5.0, C2.0, U1.-IN, U1.V-, A_Out.SLEEVE, R1.Pin_0, Trimpot.E, +BAT9V-.-, J1.GNDBREAK, J1.PWR, A_In.SLEEVE
  N2: C1.0, U1.+IN
  N3: C1.1, Trimpot.S
  N4: R3.Pin_0, C5.1
  N5: R3.Pin_1, C6.+, C4.0, U1.OUT
  N6: C6.-, A_Out.RING, A_Out.TIP
  N7: C4.1, R2.Pin_0
  N8: C2.1, U1.V+, LED1.anode, SW1.O
  N9: C3.0, C3.1, U1.GAIN, SW2.P
  N10: SW2.O, R2.Pin_1
  N11: R1.Pin_1, LED1.cathode
  N12: SW1.P, J1.GND, D1.C
  N13: Trimpot.A, A_In.TIP
  N14: +BAT9V-.+, D1.A
