# Fritzing sketch id1909_GVEP102_0 (saved by Fritzing 0.6.2b)
breadboards: 1

parts:
  7805 = voltage regulator lying
  78051 = voltage regulator lying
  +)-_7_5_DC = Power plug
  104 = Ceramic Capacitor [capacitance=100nF package="100 mil [THT, multilayer]"]
  1n4001 = Rectifier Diode [part_number=1N4001 package="300 mil [THT]"]
  S2 = SPDT-tact-small
  S3 = SPDT-tact-small
  S6 = SPDT-tact-small
  10k = Big Potentiometer
  10k_2 = Big Potentiometer
  10k_3 = Big Potentiometer
  1 = header hole
  5V = header hole
  gnd = header hole
  5V_2 = header hole
  gnd_2 = header hole
  33k = Resistor [tolerance=±5% resistance=220 package=THT]
  22k = Resistor [tolerance=±5% resistance=220 package=THT]
  33k_2 = Resistor [tolerance=±5% resistance=220 package=THT]
  22k_2 = Resistor [tolerance=±5% resistance=220 package=THT]
  33k_3 = Resistor [tolerance=±5% resistance=220 package=THT]
  22k_3 = Resistor [tolerance=±5% resistance=220 package=THT]
  1_5k = Resistor [tolerance=±5% resistance=220 package=THT]
  R = header hole
  G = header hole
  1_5k_2 = Resistor [tolerance=±5% resistance=220 package=THT]
  1_5k_3 = Resistor [tolerance=±5% resistance=220 package=THT]
  2 = header hole
  3 = header hole
  IC1 = IC, DIP package, 12 pins [chip_label=IC spacing=300mil]
  4 = header hole
  5 = header hole
  6 = header hole
  7 = header hole
  8 = header hole
  9 = header hole
  1k = Resistor [tolerance=±5% resistance=220 package=THT]
  220 = Resistor [tolerance=±5% resistance=220 package=THT]
  220_2 = Resistor [tolerance=±5% resistance=220 package=THT]
  220_3 = Resistor [tolerance=±5% resistance=220 package=THT]
  220_4 = Resistor [tolerance=±5% resistance=220 package=THT]
  1k1 = Resistor [tolerance=±5% resistance=220 package=THT]
  220_5 = Resistor [tolerance=±5% resistance=220 package=THT]
  220_6 = Resistor [tolerance=±5% resistance=220 package=THT]
  1k2 = Resistor [tolerance=±5% resistance=220 package=THT]
  gnd1 = header hole
  5V1 = header hole
  B = header hole
  220_7 = Resistor [tolerance=±5% resistance=220 package=THT]
  220_8 = Resistor [tolerance=±5% resistance=220 package=THT]
  220_9 = Resistor [tolerance=±5% resistance=220 package=THT]
  PG = header hole
  PB = header hole
  PR = header hole
  220_10 = Resistor [tolerance=±5% resistance=220 package=THT]
  220_11 = Resistor [tolerance=±5% resistance=220 package=THT]
  220_12 = Resistor [tolerance=±5% resistance=220 package=THT]
  104_2 = Ceramic Capacitor [capacitance=100nF package="100 mil [THT, multilayer]"]
  104_3 = Ceramic Capacitor [capacitance=100nF package="100 mil [THT, multilayer]"]
  104_4 = Ceramic Capacitor [capacitance=100nF package="100 mil [THT, multilayer]"]
  23 = header hole
  25 = header hole
  27 = header hole
  28 = header hole
  29 = header hole
  30 = header hole
  31 = header hole
  32 = header hole
  33 = header hole
  35 = header hole
  37 = header hole
  38 = header hole
  39 = header hole
  40 = header hole
  41 = header hole
  42 = header hole
  43 = header hole
  45 = header hole
  47 = header hole
  48 = header hole
  49 = header hole
  50 = header hole
  51 = header hole
  52 = header hole
  53 = header hole
  54 = header hole
  55 = header hole
  56 = header hole
  57 = header hole
  58 = header hole
  59 = header hole
  60 = header hole
  61 = header hole
  62 = header hole
  63 = header hole
  64 = header hole
  65 = header hole
  66 = header hole
  67 = header hole
  68 = header hole
  69 = header hole
  70 = header hole
  71 = header hole
  72 = header hole
  S7 = Pushbutton [package="[THT]"]
  73 = header hole
  74 = header hole
  75 = header hole
  76 = header hole
  78 = header hole

nets:
  N1: 7805.connector0, 78051.connector0, +)-_7_5_DC.connector0, 104.1, 1n4001.cathode
  N2: 7805.connector1, 7805.connector3, 78051.connector1, 78051.connector3, +)-_7_5_DC.connector1, +)-_7_5_DC.connector2, 104.0, 1n4001.anode, gnd.connector0, gnd_2.connector0, 22k.Pin_0, 22k_2.Pin_0, 22k_3.Pin_0, 220.Pin_1, 220_3.Pin_1, 220_5.Pin_1, gnd1.connector0
  N3: 7805.connector2, 5V.connector0
  N4: 78051.connector2, 5V_2.connector0, 33k.Pin_0, 33k_2.Pin_0, 33k_3.Pin_0, 5V1.connector0
  N5: S2.connector1, 4.connector0
  N6: S2.connector2, 1k.Pin_1
  N7: S2.connector3, 5.connector0
  N8: S3.connector1, 6.connector0
  N9: S3.connector2, 1k1.Pin_1
  N10: S3.connector3, 7.connector0
  N11: S6.connector1, 8.connector0
  N12: S6.connector2, 1k2.Pin_1
  N13: S6.connector3, 9.connector0
  N14: 10k.connector2, 33k.Pin_1
  N15: 10k.connector3, 1_5k.Pin_1
  N16: 10k.connector4, 22k_3.Pin_1
  N17: 10k_2.connector2, 33k_2.Pin_1
  N18: 10k_2.connector3, 1_5k_2.Pin_1
  N19: 10k_2.connector4, 22k.Pin_1
  N20: 10k_3.connector2, 33k_3.Pin_1
  N21: 10k_3.connector3, 1_5k_3.Pin_1
  N22: 10k_3.connector4, 22k_2.Pin_1
  N23: 1.connector0, 1_5k.Pin_0, 104_2.0
  N24: R.connector0, 220_7.Pin_0, 220_12.Pin_0
  N25: G.connector0, 220_8.Pin_0, 220_11.Pin_0
  N26: 1_5k_2.Pin_0, 2.connector0, 104_4.0
  N27: 1_5k_3.Pin_0, 3.connector0, 104_3.0
  N28: IC1.pin1, 220_2.Pin_0
  N29: IC1.pin2, 220_4.Pin_0
  N30: IC1.pin3, 220_6.Pin_1
  N31: IC1.pin4, 220_9.Pin_1
  N32: IC1.pin5, 220_8.Pin_1
  N33: IC1.pin6, 220_7.Pin_1
  N34: IC1.pin7, IC1.pin12, PR.connector0
  N35: IC1.pin8, IC1.pin11, PG.connector0
  N36: IC1.pin9, IC1.pin10, PB.connector0
  N37: 1k.Pin_0, 220.Pin_0, 220_2.Pin_1
  N38: 220_3.Pin_0, 220_4.Pin_1, 1k1.Pin_0
  N39: 220_5.Pin_0, 220_6.Pin_0, 1k2.Pin_0
  N40: B.connector0, 220_9.Pin_0, 220_10.Pin_0
  N41: 220_10.Pin_1, 104_3.1
  N42: 220_11.Pin_1, 104_4.1
  N43: 220_12.Pin_1, 104_2.1
  N44: 23.connector0, 33.connector0, 43.connector0, 70.connector0
  N45: 25.connector0, 35.connector0, 45.connector0, 65.connector0
  N46: 27.connector0, 37.connector0, 47.connector0, 71.connector0
  N47: 28.connector0, 38.connector0, 48.connector0, 69.connector0
  N48: 29.connector0, 39.connector0, 49.connector0, 66.connector0
  N49: 30.connector0, 40.connector0, 50.connector0, 64.connector0
  N50: 31.connector0, 41.connector0, 51.connector0, 68.connector0
  N51: 32.connector0, 42.connector0, 52.connector0, 62.connector0
  N52: 53.connector0, 58.connector0, 60.connector0, 72.connector0, 78.connector0
  N53: 54.connector0, 57.connector0, 61.connector0, 63.connector0, 75.connector0
  N54: 55.connector0, 56.connector0, 59.connector0, 67.connector0, 76.connector0
  N55: S7.Pin_1, S7.Pin_2, 74.connector0
  N56: S7.Pin_3, S7.Pin_4, 73.connector0
