# Fritzing sketch id190_Clock_R001_0 (saved by Fritzing 0.9.3b)
breadboards: 1

parts:
  C1 = Electrolytic Capacitor [capacitance=1µF voltage=50V package="100 mil [THT, electrolytic]"]
  LED1 = smd LED [color="Yellow (595nm)" package="1206 [SMD]"]
  R1 = Resistor [tolerance=±5% resistance=220 package="0402 [SMD]"]
  VCC1 = 4 x AAA Battery Mount
  R2 = Resistor [tolerance=±5% resistance=1 package="0402 [SMD]"]
  U1 = 555 Timer [package="DIP8 [THT]"]
  R3 = Resistor [tolerance=±5% resistance=100k package=THT]

nets:
  N1: C1.-, R1.Pin_0, VCC1.-, U1.Ground
  N2: C1.+, U1.Trigger, U1.Threshold, R3.Pin_1
  N3: LED1.cathode, U1.Output
  N4: LED1.anode, R1.Pin_1
  N5: VCC1.+, R2.Pin_1, U1.Vcc_Supply_Voltage
  N6: R2.Pin_0, U1.Discharge, R3.Pin_0
