# Fritzing sketch id1911_LED_GYRO_0 (saved by Fritzing 0.8.5b)
breadboards: 1

parts:
  Part1 = Arduino Uno (Rev3)
  LED1 = RGB LED - (4 legs) [package="5 mm [THT]"]
  IC1 = L293D [package=THT]  # not connected
  VCC1 = Battery block 9V
  GY1 = MPU-6050 GY-521 [form="♀ (female)"]

nets:
  N1: Part1.A4/SDA, GY1.connector3
  N2: Part1.A5/SCL, GY1.connector2
  N3: Part1.3V3, GY1.connector0
  N4: Part1.GND, GY1.connector1
  N5: LED1.common_anode, VCC1.+
