# Fritzing sketch id1912_MPU_6050_Arduino_0 (saved by Fritzing 0.9.2b)

parts:
  GY1 = MPU-6050 GY-521 [form="♀ (female)"]
  Composant1 = Arduino Uno (Rev3)

nets:
  N1: GY1.connector0, Composant1.5V
  N2: GY1.connector1, Composant1.GND
  N3: GY1.connector2, Composant1.A5/SCL
  N4: GY1.connector3, Composant1.A4/SDA
