# Fritzing sketch id1913_project_1_0 (saved by Fritzing 0.9.2b)

parts:
  Part1 = Arduino Yun
  R3 = Rotary Potentiometer (Small) [maximum_resistance=100kΩ package=THT]
  LCD1 = LCD screen
  LED1 = LED - 5mm [color="Red (633nm)" package="5 mm [THT]"]
  R1 = Resistor [tolerance=±5% resistance=560 package=THT]
  R4 = Resistor [tolerance=±5% resistance=220 package=THT]
  LED2 = LED - 5mm [color="Red (633nm)" package="5 mm [THT]"]
  R5 = Resistor [tolerance=±5% resistance=220 package=THT]
  LED3 = LED - 5mm [color="Red (633nm)" package="5 mm [THT]"]
  R6 = Resistor [tolerance=±5% resistance=220 package=THT]
  R7 = Resistor [tolerance=±5% resistance=220 package=THT]
  R9 = Resistor [tolerance=±5% resistance=220 package=THT]
  S1 = Pushbutton [package=THT]
  S2 = Pushbutton [package=THT]
  S3 = Pushbutton [package=THT]
  R8 = Resistor [tolerance=±5% resistance=220 package=THT]
  U1 = RELAY [package=relay-g5q]
  Solar_Cell1 = IM130407002-5V-100mA-Polycrystalline-PET-Solar-Cell [part_number=IM130407002]
  D1 = Rectifier Diode [part_number=1N4001 package="300 mil [THT]"]
  YF-S201_Flow_Meter1 = prefix0000_RichardBruneau
  JACK1 = 2.1mm_DC_Barrel_Jack
  X1 = USB Connectors [package=usb-microb]
  CONN1 = USB connector [package=THT]
  VALVE1 = Plastic_Solenoid_Valve
  YF-S201_Flow_Meter2 = prefix0000_RichardBruneau
  YF-S201_Flow_Meter3 = prefix0000_RichardBruneau
  D2 = Rectifier Diode [part_number=1N4001 package="300 mil [THT]"]
  U2 = LIPO-2000mAh [package=lipo-2000]

nets:
  5V: Part1.5V, R3.leg2, LCD1.VDD, R1.Pin_1, R7.Pin_0, R9.Pin_0, R8.Pin_0, YF-S201_Flow_Meter1.connector2
  N1: Part1.D8, LCD1.E
  N2: Part1.D9_PWM, LCD1.DB4
  N3: Part1.D10_PWM/SS, LCD1.DB5
  N4: Part1.D11_PWM/MOSI, LCD1.DB6
  N5: Part1.D12/MISO, LCD1.DB7
  GND: Part1.GND, R3.leg1, LCD1.VSS, LCD1.R/W, LCD1.LED-, LED1.anode, LED2.anode, LED3.anode, S1.leg0, S2.leg0, S3.leg0, U1.COIL2, YF-S201_Flow_Meter1.connector1
  N6: Part1.D0/RX, R9.Pin_1, S2.leg1
  N7: Part1.D1/TX, S3.leg1, R8.Pin_1
  N8: Part1.D2, R7.Pin_1, S1.leg1
  N9: Part1.D3_PWM, YF-S201_Flow_Meter1.connector0
  N10: Part1.D4, R6.Pin_1
  N11: Part1.D5_PWM, R4.Pin_1
  N12: Part1.D6_PWM, R5.Pin_1, U1.COIL1
  N13: Part1.D7, LCD1.RS
  N14: R3.wiper, LCD1.V0
  N15: LCD1.LED+, R1.Pin_0
  N16: U1.NO, VALVE1.connector2, YF-S201_Flow_Meter2.connector2
  N17: Solar_Cell1.connector0, JACK1.connector3, U2.-
  N18: D1.cathode, JACK1.connector1, D2.cathode, U2.+
  N19: X1.D+, CONN1.d+
  N20: X1.D-, CONN1.d-
  N21: X1.GND, CONN1.chassis6
  N22: X1.VBUS, CONN1.5V
  N23: VALVE1.connector1, YF-S201_Flow_Meter2.connector0
  N24: YF-S201_Flow_Meter3.connector2, D2.anode

notes:
  water pump
  dc generator turbine
