# Fritzing sketch id1914_h_bridge_0 (saved by Fritzing 0.7.4b)
breadboards: 1

parts:
  Arduino1 = Arduino
  M1 = DC Motor
  Q1 = NPN-Transistor [part_number=BC639 package="TO92 [THT]"]
  Q2 = NPN-Transistor [part_number=BC639 package="TO92 [THT]"]
  R1 = Resistor [tolerance=±5% resistance=4.7k package=THT]
  R2 = Resistor [tolerance=±5% resistance=4.7k package=THT]
  Q3 = PNP-Transistor [part_number=BC640 package="TO92 [THT]"]
  Q4 = PNP-Transistor [part_number=BC64o package="TO92 [THT]"]
  R3 = Resistor [tolerance=±5% resistance=4.7k package=THT]
  R4 = Resistor [tolerance=±5% resistance=4.7k package=THT]
  R5 = Resistor [tolerance=±5% resistance=10k package=THT]
  VCC1 = Battery block 9V
  C1 = Electrolytic Capacitor [capacitance=4.7µF voltage=50V package="100 mil [THT, electrolytic]"]
  S1 = Pushbutton [package=THT]
  Q5 = PNP-Transistor [part_number=BC640 package="TO92 [THT]"]
  R6 = Resistor [tolerance=±5% resistance=4.7k package=THT]
  Q6 = NPN-Transistor [part_number=BC547 package="TO92 [THT]"]
  R7 = Resistor [tolerance=±5% resistance=4.7k package=THT]
  R8 = Resistor [tolerance=±5% resistance=10k package=THT]

nets:
  N1: Arduino1.GND, Q1.E, Q2.E, VCC1.-, C1.-, Q6.E
  N2: Arduino1.D13, R1.Pin_1
  N3: Arduino1.D12, R2.Pin_0
  N4: Arduino1.D11, R7.Pin_0
  N5: M1.pin_1, Q1.C, Q3.C, R4.Pin_1
  N6: M1.pin_2, Q2.C, Q4.C, R3.Pin_0
  N7: Q1.B, R1.Pin_0
  N8: Q2.B, R2.Pin_1
  N9: Q3.E, Q4.E, R5.Pin_0, C1.+, S1.leg1, Q5.C
  N10: Q3.B, R3.Pin_1, R5.Pin_1
  N11: Q4.B, R4.Pin_0
  N12: VCC1.+, S1.leg0, Q5.E, R8.Pin_0
  N13: Q5.B, R6.Pin_1, R8.Pin_1
  N14: R6.Pin_0, Q6.C
  N15: Q6.B, R7.Pin_1

notes:
  P1 = pin 13
  P2 = pin 12
  P1-LOW; P2-LOW = motor stop
  P1-LOW; P2-HIGH = motor spinn in onr of direction
  P1-HIGH; P2-LOW = motor spinn in other direction
  P1-HIGH; P2-HIGH = NEVER DO THIS
  S1-OFF = PWM off
  S1-ON = PWM on
