# Fritzing sketch id1915_H_brigde_control_dc_motor_0 (saved by Fritzing 0.9.0b)
circuit board: 8.46667cm x 5.64444cm

parts:
  S1 = Pushbutton [package="[THT]"]
  S2 = Pushbutton [package="[THT]"]
  S3 = Pushbutton [package="[THT]"]
  S4 = Pushbutton [package="[THT]"]
  M1 = DC Motor
  VCC1 = Battery

nets:
  N1: S1.Pin_1, S1.Pin_2, S3.Pin_3, S3.Pin_4, M1.pin_1
  N2: S1.Pin_3, S1.Pin_4, S2.Pin_3, S2.Pin_4, VCC1.-
  N3: S2.Pin_2, S4.Pin_4, M1.pin_2
  N4: S3.Pin_1, S3.Pin_2, S4.Pin_1, S4.Pin_2, VCC1.+

notes:
  四开关H桥式电路实现直流电机正反转,按下对角开关,实现转动
