# Fritzing sketch id1916_ponte_H_com_PWM_e_pot_0 (saved by Fritzing 0.7.11b)
breadboards: 1

parts:
  Q1 = NPN-Transistor [package="TO92 [THT]"]
  Q2 = NPN-Transistor [package="TO92 [THT]"]
  R1 = Rotary Potentiometer (Small) [maximum_resistance=100kΩ]
  M1 = DC Motor
  VCC1 = Battery block 9V
  Arduino1 = Arduino
  R2 = Resistor [tolerance=±5% resistance=220 package=THT]
  R3 = Resistor [tolerance=±5% resistance=220 package=THT]
  Q3 = PNP-Transistor [package="TO92 [THT]"]
  Q4 = PNP-Transistor [package="TO92 [THT]"]
  R4 = Resistor [tolerance=±5% resistance=220 package=THT]
  R5 = Resistor [tolerance=±5% resistance=220 package=THT]

nets:
  N1: Q1.E, M1.pin_1, Q3.E
  N2: Q1.B, R2.Pin_1
  N3: Q1.C, Q2.C, R1.leg2, VCC1.-, Arduino1.GND
  N4: Q2.E, M1.pin_2, Q4.E
  N5: Q2.B, R3.Pin_0
  N6: R1.leg1, Arduino1.+5V
  N7: R1.wiper, Arduino1.A0
  N8: VCC1.+, Arduino1.VIN, Q3.C, Q4.C
  N9: Arduino1.D10, R3.Pin_1, R5.Pin_1
  N10: Arduino1.D9, R2.Pin_0, R4.Pin_0
  N11: Q3.B, R4.Pin_1
  N12: Q4.B, R5.Pin_0
