# Fritzing sketch id1918_FUNHACK_0 (saved by Fritzing 0.9.2b)
circuit board: 8.77107cm x 6.70835cm
breadboards: 1

parts:
  Part1 = Arduino Nano (Rev3.0)
  U1 = TLP621 [package=THT]
  U2 = TLP621 [package=THT]
  U3 = TLP621 [package=THT]
  U4 = TLP621 [package=THT]
  U5 = TLP621 [package=THT]
  U6 = TLP621 [package=THT]
  U7 = TLP621 [package=THT]
  U9 = TLP621 [package=THT]
  U10 = TLP621 [package=THT]
  U11 = TLP621 [package=THT]
  U12 = TLP621 [package=THT]
  J1 = female pin header, 12 pins [form="♀ (female)"]
  U8 = TLP621 [package=THT]
  J2 = female pin header, 12 pins [form="♀ (female)"]
  J3 = female pin header, 2 pins [form="♀ (female)"]

nets:
  N1: Part1.D1/TX, J3.pin2
  N2: Part1.GND, U1.Pin_1, U2.Pin_1, U3.Pin_1, U4.Pin_1, U5.Pin_1, U6.Pin_1, U7.Pin_1, U9.Pin_1, U10.Pin_1, U11.Pin_1, U12.Pin_1, U8.Pin_1, J3.pin1
  N3: Part1.D2, U1.Pin_2
  N4: Part1.D3, U2.Pin_2
  N5: Part1.D4, U3.Pin_2
  N6: Part1.D5, U4.Pin_2
  N7: Part1.D6, U5.Pin_2
  N8: Part1.D7, U6.Pin_2
  N9: Part1.D8, U7.Pin_2
  N10: Part1.D9, U8.Pin_2
  N11: Part1.D10, U9.Pin_2
  N12: Part1.D11/MOSI, U10.Pin_2
  N13: Part1.D12/MISO, U11.Pin_2
  N14: Part1.D13/SCK, U12.Pin_2
  N15: U1.Pin_4, J1.pin12
  N16: U1.Pin_3, J2.pin12
  N17: U2.Pin_4, J1.pin11
  N18: U2.Pin_3, J2.pin11
  N19: U3.Pin_4, J1.pin10
  N20: U3.Pin_3, J2.pin10
  N21: U4.Pin_4, J1.pin9
  N22: U4.Pin_3, J2.pin9
  N23: U5.Pin_4, J1.pin8
  N24: U5.Pin_3, J2.pin8
  N25: U6.Pin_4, J1.pin7
  N26: U6.Pin_3, J2.pin7
  N27: U7.Pin_4, J1.pin6
  N28: U7.Pin_3, J2.pin6
  N29: U9.Pin_4, J1.pin4
  N30: U9.Pin_3, J2.pin4
  N31: U10.Pin_4, J1.pin3
  N32: U10.Pin_3, J2.pin3
  N33: U11.Pin_4, J1.pin2
  N34: U11.Pin_3, J2.pin2
  N35: U12.Pin_4, J1.pin1
  N36: U12.Pin_3, J2.pin1
  N37: J1.pin5, U8.Pin_4
  N38: U8.Pin_3, J2.pin5

notes:
  3   3
  4   4
  5   5
  1   1
  2   2
  6   6
  7   7
  8   8
  9   9
  10   10
  11   11
  12   12
  1
  2
  3
  4
  5
  6
  7
  8
  9
  10
  11
  12
  D2-D13 ->
  <- 1-12
  Created by Renan
