# Fritzing sketch id1919_lamp_0 (saved by Fritzing 0.9.2b)
circuit board: 8.46667cm x 5.64444cm
breadboards: 1

parts:
  J5 = Power Jack [package=power_jack_combo]
  Part1 = Arduino Uno (Rev3)
  U4 = ESP8266_module [part_number=ESP8266]
  U5 = Voltage Regulator - 3.3V [package="TO220 [THT]"]
  RGB_SMD_LED1 = SMD RGB LED (WS2812) [package=5050]

nets:
  GND: J5.GND, Part1.GND, U4.connector6, U5.GND, RGB_SMD_LED1.VSS
  VIN: J5.PWR, Part1.VIN, U5.input_voltage, RGB_SMD_LED1.VDD
  N1: Part1.D11_PWM/MOSI, RGB_SMD_LED1.DIn
  N2: Part1.D2, U4.connector7
  N3: Part1.D3_PWM, U4.connector0
  N4: U4.connector1, U4.connector5, U5.output_voltage
