# Fritzing sketch id191_8LED_SN74CH595_0 (saved by Fritzing 0.9.3b)
breadboards: 1

parts:
  LED1 = LED - 3mm [color="Red (633nm)" package="3 mm [THT]"]
  LED2 = LED - 3mm [color="Red (633nm)" package="3 mm [THT]"]
  LED3 = LED - 3mm [color="Red (633nm)" package="3 mm [THT]"]
  LED4 = LED - 3mm [color="Red (633nm)" package="3 mm [THT]"]
  LED5 = LED - 3mm [color="Red (633nm)" package="3 mm [THT]"]
  LED6 = LED - 3mm [color="Red (633nm)" package="3 mm [THT]"]
  LED7 = LED - 3mm [color="Red (633nm)" package="3 mm [THT]"]
  LED8 = LED - 3mm [color="Red (633nm)" package="3 mm [THT]"]
  R1 = Resistor [tolerance=±5% resistance=330 package=THT]
  U1 = 74HC595 [package="DIP16 [THT]"]
  R2 = Resistor [tolerance=±5% resistance=330 package=THT]
  R3 = Resistor [tolerance=±5% resistance=330 package=THT]
  R4 = Resistor [tolerance=±5% resistance=330 package=THT]
  R5 = Resistor [tolerance=±5% resistance=330 package=THT]
  R6 = Resistor [tolerance=±5% resistance=330 package=THT]
  R7 = Resistor [tolerance=±5% resistance=330 package=THT]
  R8 = Resistor [tolerance=±5% resistance=330 package=THT]
  パーツ1 = Arduino Uno (Rev3)

nets:
  GND: LED1.cathode, LED2.cathode, LED3.cathode, LED4.cathode, LED5.cathode, LED6.cathode, LED7.cathode, LED8.cathode, U1.GND, U1.OE, パーツ1.GND
  N1: LED1.anode, R8.Pin_1
  N2: LED2.anode, R7.Pin_1
  N3: LED3.anode, R6.Pin_1
  N4: LED4.anode, R5.Pin_1
  N5: LED5.anode, R4.Pin_1
  N6: LED6.anode, R3.Pin_1
  N7: LED7.anode, R2.Pin_1
  N8: LED8.anode, R1.Pin_1
  N9: R1.Pin_0, U1.Q0
  N10: U1.Q1, R2.Pin_0
  N11: U1.Q2, R3.Pin_0
  N12: U1.Q3, R4.Pin_0
  N13: U1.Q4, R5.Pin_0
  N14: U1.Q5, R6.Pin_0
  N15: U1.Q6, R7.Pin_0
  N16: U1.Q7, R8.Pin_0
  VCC: U1.MR, U1.VCC, パーツ1.5V
  N17: U1.SH_CP, パーツ1.D5_PWM
  N18: U1.ST_CP, パーツ1.D6_PWM
  N19: U1.DS, パーツ1.D7
