# Fritzing sketch id1920_cheers_LED_breadbord_0 (saved by Fritzing 0.7.10b)
breadboards: 1

parts:
  LED1 = LED - 5mm [color="Red (633nm)" package="5 mm [THT]"]
  Q1 = NPN-Transistor [package="TO92 [THT]"]
  S1 = Reed switch [package=THT]
  VCC1 = Battery
  R1 = Resistor [tolerance=±5% resistance=220 package=THT]

nets:
  N1: LED1.cathode, R1.Pin_1
  N2: LED1.anode, S1.pin_1, VCC1.+
  N3: Q1.E, Q1.C, VCC1.-, R1.Pin_0
  N4: Q1.B, S1.pin_2
