# Fritzing sketch id1921_hall_effect_0 (saved by Fritzing 0.9.3b)
breadboards: 1

parts:
  Part1 = Photon
  DS1 = DS18B20 1-Wire Temperature Sensor [part_number=DS18B20]
  R1 = Resistor [tolerance=±5% resistance=1k package="2010 [SMD]"]
  R2 = Resistor [tolerance=±5% resistance=1k package="2010 [SMD]"]
  S1 = SPST Switch [package=switch-spdt]
  D1 = LTE-302 [package=lte-302]

nets:
  N1: Part1.GND, DS1.DQ, R2.Pin_1
  N2: Part1.D0, S1.O
  N3: Part1.D2, DS1.GND, R1.Pin_1
  3V3: Part1.3V3, DS1.VDD, R1.Pin_0, S1.S, D1.C
  N4: R2.Pin_0, S1.P, D1.A
