# Fritzing sketch id1923_ZS6KMD_ALC_Control_0 (saved by Fritzing 0.9.2b)
circuit board: 4.45513cm x 2.15614cm
breadboards: 1

parts:
  R1 = Rotary Potentiometer (Small) [maximum_resistance=100Ω package=THT]
  SW1 = prefix0000
  VCC1 = Battery
  R2 = Trimming Pot
  R3 = Trimming Pot
  J1 = female pin header, 2 pins [form="♀ (female)"]
  LED1 = LED - 5mm [color="Red (633nm)" package="5 mm [THT]"]
  R4 = Resistor [tolerance=±5% resistance=220 package=THT]

nets:
  N1: R1.leg1, R2.connector1
  N2: R1.wiper, J1.pin1
  N3: R1.leg2, R3.connector1
  N4: SW1.connector0, R2.connector0, R2.connector2, R4.Pin_0
  N5: SW1.connector1, VCC1.-
  N6: VCC1.+, R3.connector0, R3.connector2, J1.pin2, LED1.anode
  N7: LED1.cathode, R4.Pin_1

notes:
  ALC Contr
