# Fritzing sketch id1924_rotator_0 (saved by Fritzing 0.7.10b)
breadboards: 1

parts:
  Arduino1 = Arduino
  LCD1 = LCD screen
  RV1 = Trimmer Potentiometer [maximum_resistance=10kΩ part_number=10k package=THT]
  J1 = female pin header, 10 pins [form="♀ (female)" part_number="Control Header"]
  R2 = Resistor [tolerance=±5% resistance=1k part_number=1k package=THT]
  R3 = Resistor [tolerance=±5% resistance=1k part_number=1k package=THT]
  U1 = Voltage Regulator - 5V [package="TO220 [THT]"]
  C2 = Electrolytic Capacitor [capacitance=1µF package="100 mil [THT, electrolytic]"]
  C3 = Ceramic Capacitor [capacitance=100nF package="100 mil [THT, multilayer]"]
  C4 = Ceramic Capacitor [capacitance=100nF package="100 mil [THT, multilayer]"]
  L1 = Inductor [inductance=0.18mH current=10A part_number=180mh package="400 mil [THT]"]
  L2 = Inductor [part_number=180mh package="400 mil [THT]"]
  C1 = Electrolytic Capacitor [capacitance=0.1mF voltage=16V part_number=1000uf package="200 mil [THT, electrolytic]"]
  C5 = Electrolytic Capacitor [capacitance=1µF package="200 mil [THT, electrolytic]"]
  J3 = female pin header, 4 pins [form="♀ (female)"]
  R4 = Resistor [tolerance=±5% resistance=1k part_number=1k package=THT]
  C6 = Ceramic Capacitor [capacitance=100nF part_number=100nf package="100 mil [THT, multilayer]"]
  C7 = Electrolytic Capacitor [capacitance=1µF voltage=35V part_number=4700uf package="200 mil [THT, electrolytic]"]
  Q1 = Basic FET P-Channel [part_number=IRF9530 package="TO220 [THT]"]
  Q6 = NPN-Transistor [part_number=2N3904 package="TO92 [THT]"]
  Q7 = NPN-Transistor [part_number=2N3904 package="TO92 [THT]"]
  Q8 = NPN-Transistor [part_number=2N3904 package="TO92 [THT]"]
  Q9 = NPN-Transistor [part_number=2N3904 package="TO92 [THT]"]
  Q10 = NPN-Transistor [part_number=2N3904 package="TO92 [THT]"]
  Q11 = NPN-Transistor [part_number=2N3904 package="TO92 [THT]"]
  Q12 = NPN-Transistor [part_number=2N3904 package="TO92 [THT]"]
  Q5 = Basic FET N-Channel [part_number=IRF530 package="TO220 [THT]"]
  Q2 = Basic FET P-Channel [part_number=IRF9530 package="TO220 [THT]"]
  Q4 = Basic FET N-Channel [part_number=IRF530 package="TO220 [THT]"]
  R5 = Resistor [tolerance=±5% resistance=10k part_number=10k package=THT]
  R6 = Resistor [tolerance=±5% resistance=5.1k part_number=5.1k package=THT]
  C8 = Electrolytic Capacitor [capacitance=10µF voltage=10V part_number=10uf package="100 mil [THT, electrolytic]"]
  R7 = Resistor [tolerance=±5% resistance=10k part_number=10k package=THT]
  Z1 = Rectifier Diode [part_number=1N4001 package="300 mil [THT]"]
  R8 = Resistor [tolerance=±5% resistance=10k part_number=10k package=THT]
  R9 = Resistor [tolerance=±5% resistance=10k part_number=10k package=THT]
  R10 = Resistor [tolerance=±5% resistance=10k part_number=10k package=THT]
  R11 = Resistor [tolerance=±5% resistance=10k part_number=10k package=THT]
  R12 = Resistor [tolerance=±5% resistance=10k part_number=10k package=THT]
  R13 = Resistor [tolerance=±5% resistance=10k part_number=10k package=THT]
  R14 = Resistor [tolerance=±5% resistance=10k part_number=10k package=THT]
  R15 = Resistor [tolerance=±5% resistance=10k part_number=10k package=THT]
  R16 = Resistor [tolerance=±5% resistance=10k part_number=10k package=THT]
  R17 = Resistor [tolerance=±5% resistance=10k part_number=10k package=THT]
  R18 = Resistor [tolerance=±5% resistance=10k part_number=10k package=THT]
  Fuse1 = Fuse with Handler [part_number=Htc-15m]
  Q3 = Basic FET P-Channel [part_number=IRF9530 package="TO220 [THT]"]
  J2 = female pin header, 2 pins [form="♀ (female)" part_number=Motor]
  J4 = female pin header, 3 pins [form="♀ (female)" part_number="Rotator Pot"]

nets:
  GND: Arduino1.GND, LCD1.VSS, LCD1.R/W, RV1.leg1, J1.pin1, J1.pin3, J1.pin5, J1.pin8, U1.GND, C2.-, C3.1, C4.0, C1.-, C5.-, J3.pin1, C6.0, C7.-, Q6.E, Q7.E, Q8.E, Q9.E, Q10.E, Q11.E, Q12.E, Q5.source, Q4.source, C8.-, R7.Pin_1, Z1.cathode, J4.pin2
  N1: Arduino1.D12, LCD1.RS
  N2: Arduino1.D11, LCD1.E
  N3: Arduino1.D10, R15.Pin_1, R18.Pin_1
  N4: Arduino1.D9, R16.Pin_1, R17.Pin_1
  N5: Arduino1.D5, LCD1.DB4
  N6: Arduino1.D4, LCD1.DB5
  N7: Arduino1.D3, LCD1.DB6
  N8: Arduino1.D2, LCD1.DB7
  5V: Arduino1.+5V, R2.Pin_1, R3.Pin_1, U1.output_voltage, C4.1, C5.+, R5.Pin_0, J4.pin1
  N9: Arduino1.A0, R4.Pin_1
  N10: Arduino1.A1, J1.pin2
  N11: Arduino1.A2, J1.pin4
  N12: Arduino1.A4, J1.pin7
  N13: Arduino1.A5, J1.pin10
  N14: LCD1.VDD, RV1.leg2
  N15: LCD1.V0, RV1.wiper
  N16: J1.pin6, R3.Pin_0
  N17: J1.pin9, R2.Pin_0
  N18: U1.input_voltage, C2.+, C3.0, L2.pin_1, Z1.anode, R8.Pin_0, R9.Pin_0, R10.Pin_0, R11.Pin_0, R12.Pin_0
  N19: L1.pin_0, J3.pin4
  N20: L1.pin_1, L2.pin_0, C1.+
  N21: J3.pin2, Fuse1.Connector1
  N22: J3.pin3, C7.+, Q1.source, Fuse1.Connector2
  N23: R4.Pin_0, C6.1, J4.pin3
  N24: Q1.gate, R6.Pin_1, C8.+
  N25: Q1.drain, Q2.source, R7.Pin_0, Q3.source
  N26: Q6.B, R5.Pin_1, R10.Pin_1
  N27: Q6.C, R6.Pin_0
  N28: Q7.B, R17.Pin_0
  N29: Q7.C, Q2.gate, R8.Pin_1
  N30: Q8.B, R16.Pin_0
  N31: Q8.C, Q10.B, R14.Pin_1
  N32: Q9.B, R18.Pin_0
  N33: Q9.C, R9.Pin_1, Q3.gate
  N34: Q10.C, Q5.gate, R12.Pin_1, R14.Pin_0
  N35: Q11.B, R15.Pin_0
  N36: Q11.C, Q12.B, R13.Pin_1
  N37: Q12.C, Q4.gate, R11.Pin_1, R13.Pin_0
  N38: Q5.drain, Q3.drain, J2.pin2
  N39: Q2.drain, Q4.drain, J2.pin1

notes:
  EZ Rotator PWM Drive
  K3NG Software
  M0CKE 2012
