# Fritzing sketch id1925_pArrot_3_0 (saved by Fritzing 0.7.12b)
breadboards: 1

parts:
  IC1 = IC, DIP package, 8 pins [chip_label=IC]
  R3 = Resistor [tolerance=±5% resistance=1k package=THT]
  R4 = Resistor [tolerance=±5% resistance=47k package=THT]
  R5 = Resistor [tolerance=±5% resistance=47k package=THT]
  R1 = Resistor [tolerance=±5% resistance=1k package=THT]
  C1 = Electrolytic Capacitor [capacitance=100nF package="100 mil [THT, electrolytic]"]
  R6 = Resistor [tolerance=±5% resistance=15k package=THT]
  R7 = Resistor [tolerance=±5% resistance=33k package=THT]
  R8 = Trimmer Potentiometer [maximum_resistance=10kΩ package=THT]
  D1 = Rectifier Diode [part_number=1N4148 package="300 mil [THT]"]
  C2 = Electrolytic Capacitor [capacitance=47µF package="100 mil [THT, electrolytic]"]
  R8_2 = Resistor [tolerance=±5% resistance=4.7k package=THT]
  R9 = Resistor [tolerance=±5% resistance=2.2k package=THT]
  Q1 = NPN-Transistor [part_number=BC548 package="TO92 [THT]"]
  R10 = Resistor [tolerance=±5% resistance=3.9k package=THT]
  R11 = Resistor [tolerance=±5% resistance=3.9k package=THT]
  Q2 = PNP-Transistor [package="TO92 [THT]"]
  LED1 = LED - 5mm [color="Red (633nm)" package="5 mm [THT]"]
  R12 = Resistor [tolerance=±5% resistance=220 package=THT]
  R13 = Resistor [tolerance=±5% resistance=10k package=THT]
  J1 = Screw terminal - 2 pins [package=THT]
  C3 = Electrolytic Capacitor [capacitance=100nF package="100 mil [THT, electrolytic]"]
  R14 = Resistor [tolerance=±5% resistance=10k package=THT]
  J2 = Screw terminal - 2 pins [package=THT]
  J3 = female pin header, 2 pins [form="♀ (female)"]
  C4 = Ceramic Capacitor [capacitance=10nF package="100 mil [THT, multilayer]"]
  J5 = Screw terminal - 2 pins [package=THT]
  J6 = female pin header, 3 pins [form="♀ (female)"]
  J4 = screw terminal, 3 pins
  Q3 = NPN-Transistor [package="TO92 [THT]"]
  C5 = Ceramic Capacitor [capacitance=10nF package="100 mil [THT, multilayer]"]

nets:
  N1: IC1.pin1, IC1.pin5, R3.Pin_0
  N2: IC1.pin2, R3.Pin_1, R1.Pin_0
  N3: IC1.pin3, R4.Pin_1, R5.Pin_0
  GND: IC1.pin4, R5.Pin_1, R7.Pin_1, C2.-, R9.Pin_1, Q1.E, R12.Pin_1, R13.Pin_1, J1.pin1, R14.Pin_1, J2.pin1, J3.pin1, J4.pin1, Q3.E, C5.0
  N4: IC1.pin6, R8.wiper
  N5: IC1.pin7, D1.anode
  5V: IC1.pin8, R4.Pin_0, R6.Pin_0, R10.Pin_0, Q2.E, J3.pin2
  N6: R1.Pin_1, C1.-, R13.Pin_0
  N7: C1.+, J1.pin2, C3.+
  N8: R6.Pin_1, R8.leg2
  N9: R7.Pin_0, R8.leg1
  N10: D1.cathode, C2.+, R8_2.Pin_1
  N11: R8_2.Pin_0, R9.Pin_0, Q1.B
  N12: Q1.C, R11.Pin_1
  N13: R10.Pin_1, R11.Pin_0, Q2.B
  N14: Q2.C, LED1.anode, J6.pin3
  N15: LED1.cathode, R12.Pin_0
  N16: C3.-, R14.Pin_0, J2.pin2
  N17: C4.0, J4.pin3
  N18: C4.1, J5.pin1, J6.pin1
  N19: J5.pin2, C5.1
  N20: J6.pin2, Q3.B
  N21: J4.pin2, Q3.C

notes:
  Audio in
  Audio out (to mic ISD1820)
  Audio out to TRX
  5V power from Arduino
  pArrot repeater, Parrot repeater based on Arduino Uno and ISD1820, 1
