# Fritzing sketch id1926_esquema_circuit_0 (saved by Fritzing 0.9.3b)

parts:
  Componente1 = Arduino Nano (Rev3.0) (ICSP)
  U2 = G3VM-61E1 [package=g3vm-61e1]
  J1 = Peltier Element
  R1 = Resistor [tolerance=±5% resistance=220 package="2512 [SMD]"]
  R2 = Resistor [tolerance=±5% resistance=220 package="2512 [SMD]"]
  R3 = Resistor [tolerance=±5% resistance=220 package="2512 [SMD]"]
  U3 = BATTERY-2 [package=battery-aaa]
  F1 = fan_Ventilador  # not connected
  LED1 = LED - 5mm [color="Red (633nm)" package="5 mm [THT]"]
  LED2 = smd LED [color="Yellow (585nm)" package="0603 [SMD]"]
  R4 = Resistor [tolerance=±5% resistance=220 package="2512 [SMD]"]
  LED3 = LED - 5mm [color="Green (555nm)" package="5 mm [THT]"]
  RHT2 = prefix0000

nets:
  N1: Componente1.GND, RHT2.connector10
  N2: Componente1.D3, R4.Pin_1
  N3: Componente1.D4, R2.Pin_1
  N4: Componente1.D5, R1.Pin_1
  N5: Componente1.D6, U2.P$6
  N6: U2.P$1, J1.pin2
  N7: U2.P$2, U3.+1
  N8: J1.pin1, U3.-1
  N9: R1.Pin_0, LED2.anode
  N10: R2.Pin_0, LED3.anode
  N11: R3.Pin_0, RHT2.connector8
  N12: R3.Pin_1, RHT2.connector9
  N13: LED1.anode, R4.Pin_0
