# Fritzing sketch id1927_Untitled_Sketch_0 (saved by Fritzing 0.9.0b)
breadboards: 1

parts:
  R1 = Rotary Potentiometer (Small) [maximum_resistance=100kΩ package=THT]
  R2 = Photocell (LDR) [package=THT]
  R3 = Photocell (LDR) [package=THT]
  R4 = Photocell (LDR) [package=THT]
  LCD1 = LCD screen
  Part1 = Arduino Leonardo (Rev3b)
  R5 = Resistor [tolerance=±5% resistance=220 package=THT]
  R7 = Resistor [tolerance=±5% resistance=220 package=THT]
  R6 = Resistor [tolerance=±5% resistance=220 package=THT]
  R8 = Resistor [tolerance=±5% resistance=220 package=THT]

nets:
  VSS: R1.leg1, LCD1.VSS, LCD1.R/W, LCD1.LED-, Part1.GND, R5.Pin_0, R7.Pin_1, R6.Pin_0
  N1: R1.wiper, LCD1.V0
  VDD: R1.leg2, R2.pin_1, R3.pin_1, R4.pin_0, LCD1.VDD, Part1.5V, R8.Pin_0
  N2: R2.pin_0, Part1.A2, R6.Pin_1
  N3: R3.pin_0, Part1.A1, R5.Pin_1
  N4: R4.pin_1, Part1.A0, R7.Pin_0
  N5: LCD1.RS, Part1.D7
  N6: LCD1.E, Part1.D6_PWM/A7
  N7: LCD1.DB4, Part1.D5_PWM
  N8: LCD1.DB5, Part1.D4/A6
  N9: LCD1.DB6, Part1.D3_PWM/SCL
  N10: LCD1.DB7, Part1.D2/SDA
  N11: LCD1.LED+, R8.Pin_1
