# Fritzing sketch id1928_Android_Equivelant_using_ATMega_0 (saved by Fritzing 0.7.4b)
breadboards: 1

parts:
  Arduino1 = Arduino Mini
  U1 = atmega328 [package=dip]
  LED1 = LED - 5mm [color="Red (633nm)" package="5 mm [THT]"]  # not connected
  R1 = Resistor [tolerance=±5% resistance=220 package=THT]
  R2 = Resistor [tolerance=±5% resistance=220 package=THT]
  S1 = Pushbutton [package="[THT]"]
  R3 = Resistor [tolerance=±5% resistance=220 package=THT]
  LED2 = LED - 5mm [color="Red (633nm)" package="5 mm [THT]"]
  R4 = Resistor [tolerance=±5% resistance=220 package=THT]
  U2 = Voltage Regulator - Variable [package="TO220 [THT]"]
  C1 = Electrolytic Capacitor [capacitance=1µF package="100 mil [THT, electrolytic]"]
  C2 = Electrolytic Capacitor [capacitance=1µF package="100 mil [THT, electrolytic]"]
  Power_plug1 = Power plug

nets:
  +5V: Arduino1.+5V, U1.VCC, U1.AVCC, U1.AREF, R2.Pin_0, R3.Pin_0, U2.IN, C1.+
  N1: Arduino1.RST, R2.Pin_1
  GND: Arduino1.GND, U1.GND, R1.Pin_0, S1.Pin_3, S1.Pin_4, R4.Pin_0, U2.OUT, C1.-, C2.-, Power_plug1.GND
  N2: U1.RESET, S1.Pin_1, S1.Pin_2, R3.Pin_1
  N3: LED2.cathode, R4.Pin_1
  N4: U2.ADJ, C2.+, Power_plug1.VCC

notes:
  5 Volts
  3 Volts
