# Fritzing sketch id1929_animated_birthday_card_0 (saved by Fritzing 0.7.4b)
breadboards: 1

parts:
  Animated_birthday_card = LilyPad Arduino Simple Board
  Resistor = Resistor [tolerance=±5% resistance=220 package=THT]
  Resistor_2 = Resistor [tolerance=±5% resistance=220 package=THT]
  Piezo_Speaker = Piezo Speaker
  Reed_Switch = Reed switch [package=THT]
  Diffused_LED = LED - 5mm [color="Yellow (592nm)" package="5 mm [THT]"]
  Diffused_LED_2 = LED - 5mm [color="Yellow (592nm)" package="5 mm [THT]"]
  Resistor_3 = Resistor [tolerance=±5% resistance=10k package=THT]

nets:
  N1: Animated_birthday_card.VCC, Resistor_3.Pin_0
  N2: Animated_birthday_card.GND, Resistor.Pin_0, Resistor_2.Pin_0, Piezo_Speaker.pin2, Reed_Switch.pin_2
  N3: Animated_birthday_card.D6, Diffused_LED_2.anode
  N4: Animated_birthday_card.D9, Piezo_Speaker.pin1
  N5: Animated_birthday_card.D10, Reed_Switch.pin_1, Resistor_3.Pin_1
  N6: Animated_birthday_card.D5, Diffused_LED.anode
  N7: Resistor.Pin_1, Diffused_LED.cathode
  N8: Resistor_2.Pin_1, Diffused_LED_2.cathode
