# Fritzing sketch id192_TC802C_Test_0 (saved by Fritzing 0.9.0b)
breadboards: 1

parts:
  Eleman1 = Arduino Uno (Rev3) - ICSP
  B20K_dan_B50K_ya_kadar_Timpot_yada_Potansiyometre = TRIMPOT [package=3386u]
  TC802C-03_8X2_LCD = prefix0000

nets:
  N1: Eleman1.ICSP_MISO, Eleman1.D12/MISO, TC802C-03_8X2_LCD.connector3
  N2: Eleman1.D10_PWM/SS, TC802C-03_8X2_LCD.connector5
  N3: Eleman1.D2, TC802C-03_8X2_LCD.connector13
  N4: Eleman1.D3_PWM, TC802C-03_8X2_LCD.connector12
  N5: Eleman1.D4, TC802C-03_8X2_LCD.connector11
  N6: Eleman1.D5_PWM, TC802C-03_8X2_LCD.connector10
  N7: Eleman1.5V, B20K_dan_B50K_ya_kadar_Timpot_yada_Potansiyometre.CCW, TC802C-03_8X2_LCD.connector1
  N8: Eleman1.GND, B20K_dan_B50K_ya_kadar_Timpot_yada_Potansiyometre.CW, TC802C-03_8X2_LCD.connector0, TC802C-03_8X2_LCD.connector4
  N9: B20K_dan_B50K_ya_kadar_Timpot_yada_Potansiyometre.WIPER, TC802C-03_8X2_LCD.connector2

notes:
  LCD Ekranda sol at pin 1
  Sol üst Pin 2
  Sol Alttan 2 inci 3. pindir bu şekilde gider
  Not Lcd baglantısında LCD üzerinde sağ tuş yapup pinlerin isimlerine bakmanızı tavsiye ederim. Pinler doğru yerde fakat TC802C LCD'de sağ altlı üstlü 2 pin bulunmamaktadır.
