# Fritzing sketch id1933_HBridge_0 (saved by Fritzing 0.7.10b)
breadboards: 1

parts:
  Q3 = NPN-Transistor [package="TO92 [THT]"]
  M1 = DC Motor
  Q4 = NPN-Transistor [package="TO92 [THT]"]
  VCC1 = Battery
  D1 = Rectifier Diode [part_number=1N4001 package="300 mil [THT]"]
  D3 = Rectifier Diode [part_number=1N4001 package="300 mil [THT]"]
  D2 = Rectifier Diode [part_number=1N4001 package="300 mil [THT]"]
  D4 = Rectifier Diode [part_number=1N4001 package="300 mil [THT]"]
  Arduino1 = Arduino
  Q1 = NPN-Transistor [package="TO92 [THT]"]
  Q2 = NPN-Transistor [package="TO92 [THT]"]

nets:
  N1: Q3.E, M1.pin_2, Q4.C, D3.anode, D4.cathode
  N2: Q3.B, Arduino1.D3
  N3: Q3.C, VCC1.+, D1.cathode, D3.cathode, Q1.C
  N4: M1.pin_1, D1.anode, D2.cathode, Q1.E, Q2.C
  N5: Q4.E, VCC1.-, D2.anode, D4.anode, Arduino1.GND, Q2.E
  N6: Q4.B, Arduino1.D4
  N7: Arduino1.D6, Q2.B
  N8: Arduino1.D5, Q1.B
