# Fritzing sketch id1934_hc_05_serial_0 (saved by Fritzing 0.9.2b)

parts:
  Part1 = Bluetooth HC-05 Macho
  Onderdeel1 = Arduino Mega 2560 (Rev3)
  LED1 = RGB LED (com. cathode, rgb) [package="5 mm [THT]"]
  R1 = Resistor [tolerance=±5% resistance=220 package="2512 [SMD]"]

nets:
  N1: Part1.TXD, Onderdeel1.D1_TX0
  N2: Part1.RXD, Onderdeel1.D0_RX0
  VCC: Part1.VCC, Onderdeel1.5V
  N3: Onderdeel1.GND, R1.Pin_0
  N4: Onderdeel1.D5_PWM, LED1.green_anode
  N5: Onderdeel1.D6_PWM, LED1.blue_anode
