# Fritzing sketch id1936_HC_05_06_0 (saved by Fritzing 0.9.2b)
circuit board: 8.46667cm x 5.64444cm
breadboards: 1

parts:
  U2 = mystery part, 4 pins [chip_label=HC-05]
  J1 = screw terminal, 3 pins
  U1 = attiny85 [package=dip]

nets:
  N1: U2.pin1, U1.Pin_1
  N2: U2.pin2, U1.Pin_2
  N3: U2.pin3, U2.pin4, J1.pin2, J1.pin3, U1.Pin_4, U1.Pin_8
  N4: J1.pin1, U1.Pin_6
