# Fritzing sketch id1937_HC_05_Test_0 (saved by Fritzing 0.9.3b)
circuit board: 8.46667cm x 5.64444cm
breadboards: 1

parts:
  Componente1 = Arduino Due (Rev2b)
  Componente2 = Bluetooth HC-05 Macho
  R2 = Resistor [tolerance=±5% resistance=1.5k package=THT]
  R3 = Resistor [tolerance=±5% resistance=1.2k package=THT]
  R4 = Resistor [tolerance=±5% resistance=330 package=THT]

nets:
  5V: Componente1.5V, Componente2.VCC
  GND: Componente1.GND, Componente2.GND, R2.Pin_0, R3.Pin_0
  N1: Componente1.D10_PWM/SS0, Componente2.TXD
  N2: Componente1.D11_PWM, Componente2.Key, R4.Pin_1
  N3: Componente2.RXD, R2.Pin_1, R3.Pin_1, R4.Pin_0
