# Fritzing sketch id1938_HC_SR04_0 (saved by Fritzing 0.9.2b)

parts:
  Bauteil1 = Arduino Uno (Rev3)
  U2 = generic_sip_4_300mil.fzp [chip_label=IC]

nets:
  N1: Bauteil1.D2, U2.connector2
  N2: Bauteil1.D3_PWM, U2.connector1
  N3: Bauteil1.5V, U2.connector0
  N4: Bauteil1.GND, U2.connector3
