# Fritzing sketch id1939_ultrasonic_alarm_0 (saved by Fritzing 0.9.3b)
breadboards: 1

parts:
  Part1 = Arduino Uno (Rev3)
  hc-sr1 = hc-sr04
  J1 = Piezo Speaker
  LED1 = LED - 5mm [color="Red (633nm)" package="5 mm [THT]"]
  R1 = Resistor [tolerance=±5% resistance=220 package=THT]

nets:
  N1: Part1.D9_PWM, hc-sr1.Trig
  N2: Part1.D10_PWM/SS, hc-sr1.Echo
  N3: Part1.D11_PWM/MOSI, J1.pin2
  N4: Part1.D13/SCK, R1.Pin_1
  5V: Part1.5V, hc-sr1.VCC
  GND: Part1.GND, hc-sr1.GND, J1.pin1, LED1.cathode
  N5: LED1.anode, R1.Pin_0
