# Fritzing sketch id193_ArduinoFritzing_0 (saved by Fritzing 0.9.3b)
breadboards: 1

parts:
  Часть1 = Arduino Mega 2560 (Rev3)
  Disp1 = LBT2088AH [part_number=LBT2088AH]
  U1 = Thumb Joystick [package=joystick]
  U2 = Thumb Joystick [package=joystick]
  Disp2 = LBT2088AH [part_number=LBT2088AH]

nets:
  N1: Часть1.A0, U2.V-
  N2: Часть1.A1, U1.V-
  N3: Часть1.D12_PWM, Disp1.pin_3
  N4: Часть1.D11_PWM, Disp1.pin_5
  N5: Часть1.D10_PWM, Disp1.pin_4
  N6: Часть1.D9_PWM, Disp2.pin_3
  N7: Часть1.D8_PWM, Disp2.pin_5
  N8: Часть1.3V3, Disp2.pin1
  N9: Часть1.5V, Disp1.pin1, U1.H-, U2.H-
  N10: Часть1.GND, Disp1.pin2, U1.H, U2.H, Disp2.pin2
  N11: Часть1.D7_PWM, Disp2.pin_4
