# Fritzing sketch id1940_sonar_led_leo_0 (saved by Fritzing 0.8.3b)
breadboards: 1

parts:
  Εξάρτημα1 = SRF05 Ultrasonic Rangefinder
  Εξάρτημα2 = Arduino Leonardo (Rev3b)
  LED1 = LED - 5mm [color="Red (633nm)" package="5 mm [THT]"]
  LED2 = LED - 5mm [color="Red (633nm)" package="5 mm [THT]"]
  LED3 = LED - 5mm [color="Red (633nm)" package="5 mm [THT]"]
  LED4 = LED - 5mm [color="Red (633nm)" package="5 mm [THT]"]
  LED5 = LED - 5mm [color="Red (633nm)" package="5 mm [THT]"]
  LED6 = LED - 5mm [color="Red (633nm)" package="5 mm [THT]"]
  LED7 = LED - 5mm [color="Red (633nm)" package="5 mm [THT]"]
  LED8 = LED - 5mm [color="Red (633nm)" package="5 mm [THT]"]
  LED9 = LED - 5mm [color="Red (633nm)" package="5 mm [THT]"]
  LED10 = LED - 5mm [color="Red (633nm)" package="5 mm [THT]"]
  R1 = Resistor [tolerance=±5% resistance=220 package=THT]
  R2 = Resistor [tolerance=±5% resistance=220 package=THT]
  R3 = Resistor [tolerance=±5% resistance=220 package=THT]
  R4 = Resistor [tolerance=±5% resistance=220 package=THT]
  R5 = Resistor [tolerance=±5% resistance=220 package=THT]
  R6 = Resistor [tolerance=±5% resistance=220 package=THT]
  R7 = Resistor [tolerance=±5% resistance=220 package=THT]
  R8 = Resistor [tolerance=±5% resistance=220 package=THT]
  R9 = Resistor [tolerance=±5% resistance=220 package=THT]
  R10 = Resistor [tolerance=±5% resistance=220 package=THT]

nets:
  N1: Εξάρτημα1.connector8, Εξάρτημα2.5V
  N2: Εξάρτημα1.connector9, Εξάρτημα2.D12/A11
  N3: Εξάρτημα1.connector10, Εξάρτημα2.D13_PWM
  N4: Εξάρτημα1.connector11, Εξάρτημα2.GND, R1.Pin_1, R2.Pin_1, R3.Pin_1, R4.Pin_1, R5.Pin_1, R6.Pin_1, R7.Pin_1, R8.Pin_1, R9.Pin_1, R10.Pin_1
  N5: Εξάρτημα2.D2/SDA, LED7.cathode
  N6: Εξάρτημα2.D3_PWM/SCL, LED6.cathode
  N7: Εξάρτημα2.D4/A6, LED5.cathode
  N8: Εξάρτημα2.D5_PWM, LED4.cathode
  N9: Εξάρτημα2.D6_PWM/A7, LED9.cathode
  N10: Εξάρτημα2.D7, LED8.cathode
  N11: Εξάρτημα2.D8/A8, LED10.cathode
  N12: Εξάρτημα2.D9_PWM/A9, LED3.cathode
  N13: Εξάρτημα2.D10_PWM/A10, LED1.cathode
  N14: Εξάρτημα2.D11_PWM, LED2.cathode
  N15: LED1.anode, R2.Pin_0
  N16: LED2.anode, R1.Pin_0
  N17: LED3.anode, R3.Pin_0
  N18: LED4.anode, R7.Pin_0
  N19: LED5.anode, R8.Pin_0
  N20: LED6.anode, R9.Pin_0
  N21: LED7.anode, R10.Pin_0
  N22: LED8.anode, R5.Pin_0
  N23: LED9.anode, R6.Pin_0
  N24: LED10.anode, R4.Pin_0
