# Fritzing sketch id1941_HC_SR04_0 (saved by Fritzing 0.9.2b)

parts:
  Parte1 = Arduino Mega 2560 (Rev3)
  Parte2 = SRF05 Ultrasonic Rangefinder

nets:
  N1: Parte1.D12_PWM, Parte2.connector9
  N2: Parte1.D11_PWM, Parte2.connector10
  N3: Parte1.5V, Parte2.connector8
  N4: Parte1.GND, Parte2.connector11
