# Fritzing sketch id1944_HC_SR04_Example_0 (saved by Fritzing 0.9.0b)
breadboards: 1

parts:
  U1 = generic_sip_4_300mil.fzp [chip_label=IC]
  Part1 = Arduino Uno (Rev3)
  LED2 = smd LED [color="Red (633nm)" package="0603 [SMD]"]
  R1 = Resistor [tolerance=±5% resistance=220 package="1206 [SMD]"]
  R2 = Resistor [tolerance=±5% resistance=220 package="1206 [SMD]"]
  LED4 = smd LED [color="Red (633nm)" package="1206 [SMD]"]

nets:
  N1: U1.connector0, Part1.5V
  N2: U1.connector1, Part1.D12/MISO
  N3: U1.connector2, Part1.D6_PWM
  N4: U1.connector3, Part1.GND, LED2.cathode, LED4.cathode
  N5: Part1.D8, R1.Pin_0
  N6: Part1.D10_PWM/SS, R2.Pin_1
  N7: LED2.anode, R1.Pin_1
  N8: R2.Pin_0, LED4.anode
