# Fritzing sketch id1945_HC_SR501_Arduino_0 (saved by Fritzing 0.9.3b)

parts:
  Arduino_UNO = Arduino Uno (Rev3)
  Sensore_PIR_HC-SR501 = PIR D-SUN HC-SR501
  LED = LED - 5mm [color="Red (633nm)" package="5 mm [THT]"]

nets:
  N1: Arduino_UNO.D13/SCK, LED.anode
  N2: Arduino_UNO.GND, Sensore_PIR_HC-SR501.connector2, LED.cathode
  N3: Arduino_UNO.D2, Sensore_PIR_HC-SR501.connector1
  N4: Arduino_UNO.5V, Sensore_PIR_HC-SR501.connector0
