# Fritzing sketch id1946_4094_test_0 (saved by Fritzing 0.9.2b)
breadboards: 1

parts:
  Part1 = Arduino Mega 2560 (Rev3)
  HEF1 = HEF4094 [package="DIP16 [THT]"]
  LED1 = LED - 3mm [color="Red (633nm)" package="3 mm [THT]"]
  R1 = Resistor [tolerance=±5% resistance=220 package="1206 [SMD]"]
  R2 = Resistor [tolerance=±5% resistance=220 package="1206 [SMD]"]
  R3 = Resistor [tolerance=±5% resistance=220 package="1206 [SMD]"]
  LED2 = LED - 3mm [color="Red (633nm)" package="3 mm [THT]"]
  LED3 = LED - 3mm [color="Red (633nm)" package="3 mm [THT]"]  # not connected
  IC1 = ULN2003A [package="DIP16 [THT]"]

nets:
  5V: Part1.5V, HEF1.OE, HEF1.Vdd
  GND: Part1.GND, HEF1.Vss, R1.Pin_0, R2.Pin_0, R3.Pin_0, IC1.In_7
  N1: Part1.D5_PWM, HEF1.STROBE
  N2: Part1.D6_PWM, HEF1.DATA
  N3: Part1.D7_PWM, HEF1.CLOCK
  N4: HEF1.Q1, IC1.Out_1
  N5: HEF1.Q2, IC1.Out_3
  N6: HEF1.Q3, IC1.Out_5
  N7: LED1.cathode, IC1.In_1
  N8: LED1.anode, R1.Pin_1, IC1.In_2
  N9: R2.Pin_1, LED2.anode, IC1.In_4
  N10: R3.Pin_1, IC1.In_6
  N11: LED2.cathode, IC1.In_3
