# Fritzing sketch id1947_montage_V3_0 (saved by Fritzing 0.9.2b)
breadboards: 1

parts:
  U2 = MIC [package=mic-9.7mm]
  U3 = LM 358 Dual Op-Amp [package="DIP8 [THT]"]
  R20 = Resistor [tolerance=±5% resistance=1M package="0805 [SMD]"]
  R21 = Resistor [tolerance=±5% resistance=3.3k package="0805 [SMD]"]
  R22 = Resistor [tolerance=±5% resistance=10k package="0805 [SMD]"]
  R23 = Resistor [tolerance=±5% resistance=10k package="0805 [SMD]"]
  R24 = Resistor [tolerance=±5% resistance=10k package="0805 [SMD]"]
  C2 = Electrolytic Capacitor [capacitance=100µF package="0405 [SMD, electrolytic]"]
  U4 = LM 358 Dual Op-Amp [package="DIP8 [THT]"]
  Composant1 = Arduino Uno (Rev3)
  SP1 = SPEAKER [package=pcb_mount_speaker]
  U8 = LM 358 Dual Op-Amp [package="DIP8 [THT]"]
  U9 = POT [package=alps_pot]
  C7 = Ceramic Capacitor [capacitance=10µF package="1206 [SMD, multilayer]"]
  U10 = POT [package=alps_pot]
  C8 = Ceramic Capacitor [capacitance=10µF package="1206 [SMD, multilayer]"]
  U12 = LM 358 Dual Op-Amp [package="DIP8 [THT]"]
  U13 = LM 358 Dual Op-Amp [package="DIP8 [THT]"]
  R25 = Resistor [tolerance=±5% resistance=220 package="0805 [SMD]"]
  R26 = Resistor [tolerance=±5% resistance=220 package="0805 [SMD]"]
  R27 = Resistor [tolerance=±5% resistance=220 package="0805 [SMD]"]
  R28 = Resistor [tolerance=±5% resistance=220 package="0805 [SMD]"]
  U14 = LM 358 Dual Op-Amp [package="DIP8 [THT]"]
  R29 = Resistor [tolerance=±5% resistance=220 package=THT]
  R30 = Resistor [tolerance=±5% resistance=220 package=THT]
  C9 = Electrolytic Capacitor [capacitance=1µF package="100 mil [THT, electrolytic]"]
  C10 = Electrolytic Capacitor [capacitance=100µF package="0405 [SMD, electrolytic]"]
  R31 = Resistor [tolerance=±5% resistance=82 package="0805 [SMD]"]
  R32 = Resistor [tolerance=±5% resistance=62k package="0805 [SMD]"]
  C11 = Tantalum Capacitor [capacitance=100nF package="100 mil [THT, tantalum]"]
  C12 = Tantalum Capacitor [capacitance=100nF package="100 mil [THT, tantalum]"]
  C13 = Capacitor Polarized [package=panasonic_c]
  R33 = Resistor [tolerance=±5% resistance=100k package="0805 [SMD]"]
  R34 = Resistor [tolerance=±5% resistance=100k package="0805 [SMD]"]
  V15 = DC Power [voltage=3V]
  R35 = Resistor [tolerance=±5% resistance=220 package=THT]
  R36 = Resistor [tolerance=±5% resistance=220 package=THT]
  C14 = Electrolytic Capacitor [capacitance=1µF package="100 mil [THT, electrolytic]"]
  U17 = LM 358 Dual Op-Amp [package="DIP8 [THT]"]
  R37 = Resistor [tolerance=±5% resistance=220 package=THT]
  R38 = Resistor [tolerance=±5% resistance=220 package=THT]
  U19 = LM 358 Dual Op-Amp [package="DIP8 [THT]"]
  C15 = Electrolytic Capacitor [capacitance=1µF package="100 mil [THT, electrolytic]"]
  C16 = Electrolytic Capacitor [capacitance=1µF package="100 mil [THT, electrolytic]"]
  U20 = LM 358 Dual Op-Amp [package="DIP8 [THT]"]
  R39 = Resistor [tolerance=±5% resistance=220 package=THT]
  R40 = Resistor [tolerance=±5% resistance=220 package=THT]
  R41 = Resistor [tolerance=±5% resistance=220 package=THT]
  R42 = Resistor [tolerance=±5% resistance=220 package=THT]
  R43 = Resistor [tolerance=±5% resistance=220 package=THT]
  R44 = Resistor [tolerance=±5% resistance=390 package=THT]
  R45 = Resistor [tolerance=±10% resistance=3.2k package=THT]

nets:
  GND: U2.1, R23.Pin_1, C2.-, SP1.-, U8.connector3, C7.0, U10.E, U12.connector3, U13.connector3, R26.Pin_1, R29.Pin_0, C9.-, R32.Pin_0, C11.-, R35.Pin_0, U19.connector2, R43.Pin_1, R44.Pin_1
  N1: U2.2, R24.Pin_1, C10.+
  N2: U3.connector0, U3.connector4, R20.Pin_1
  N3: U3.connector1, R20.Pin_0, R21.Pin_1
  N4: U3.connector2, R22.Pin_1, R23.Pin_0
  -1.5V: U3.connector3, U4.connector3, U14.connector3, C13.-, R33.Pin_1, V15.V-, U17.connector3, U19.connector3, U20.connector3
  N5: U3.connector5, U3.connector6, R31.Pin_0
  1.5V: U3.connector7, U4.connector7, U14.connector7, R34.Pin_0, V15.V+, U17.connector7, U19.connector7, U20.connector7
  N6: R21.Pin_0, C10.-
  3.3V: R22.Pin_0, R24.Pin_0, C2.+, U8.connector7, U12.connector7, U13.connector7
  N7: U4.connector0, U4.connector1, U14.connector4, U17.connector4, U19.connector4
  N8: U4.connector2, R32.Pin_1, C12.+
  N9: U4.connector4, R31.Pin_1
  N10: U4.connector5, U4.connector6, C11.+, C12.-
  N11: Composant1.D1/TX, U13.connector0, U13.connector1
  N12: Composant1.D2, U9.S
  N13: Composant1.D3_PWM, U10.S
  N14: Composant1.D4, U8.connector4
  N15: SP1.+, U20.connector5, U20.connector6
  N16: U8.connector0, U8.connector1, U9.A
  N17: U8.connector2, U8.connector5, U8.connector6, C8.0
  N18: U9.E, C7.1, U12.connector2
  N19: U10.A, C8.1, U12.connector4
  N20: U12.connector0, U12.connector1, R28.Pin_0
  N21: U12.connector5, U12.connector6, R27.Pin_0
  N22: U13.connector2, U13.connector6, R25.Pin_1
  N23: U13.connector4, R27.Pin_1, R28.Pin_1
  N24: U13.connector5, R25.Pin_0, R26.Pin_0
  N25: U14.connector0, R30.Pin_1
  N26: U14.connector1, R29.Pin_1, R30.Pin_0
  N27: U14.connector2, C9.+, R45.Pin_0
  N28: U14.connector5, U14.connector6, R40.Pin_0, R45.Pin_1
  0V: C13.+, R33.Pin_0, R34.Pin_1
  N29: R35.Pin_1, R36.Pin_0, U17.connector1
  N30: R36.Pin_1, U17.connector0
  N31: C14.-, U17.connector2, R44.Pin_0
  N32: C14.+, U17.connector5, U17.connector6, R39.Pin_0
  N33: R37.Pin_0, U19.connector5, U19.connector6, R41.Pin_0
  N34: R37.Pin_1, C15.+
  N35: R38.Pin_0, U19.connector1, C15.-, C16.+
  N36: R38.Pin_1, U19.connector0, C16.-
  N37: U20.connector0, U20.connector4, R42.Pin_1
  N38: U20.connector1, R39.Pin_1, R40.Pin_1, R41.Pin_1
  N39: U20.connector2, R42.Pin_0, R43.Pin_0

notes:
  Passe bas avec gain
  gain :  (R29+R30)/R29
  fc = 1/(2*pi*R*C)
  Passe haut avec gain
  gain :  (R25+R36)/R25
  Coupe bande
  Alimentation Symetrique a partir de la pile
  Passe bande avec gain
  res et condo non dimentionné
  res non dimentionné
