# Fritzing sketch id1949_Pulse1_wTooGoo_0 (saved by Fritzing 0.9.3b)
circuit board: 9.00001cm x 5.99999cm
breadboards: 1

parts:
  RESET = Momentary Switch [package=tactile-pth]
  TrimPot = Trimmer Potentiometer [maximum_resistance=10kΩ package=THT]
  NANO = Arduino Nano (Rev3.0)
  BATT = female pin header, 2 pins [form="♀ (female)"]
  INK1 = Nokia_5110_R2 [part_number="Nokia 5110"]
  LED_BLINK = female pin header, 2 pins [form="♀ (female)"]
  SW1 = slide_switch_new R1
  C1 = Capacitor [package=cap-pth-small-kit]
  R1 = Resistor [tolerance=±5% resistance=200 package=THT]
  PULSE1 = female pin header, 3 pins [form="♀ (female)"]
  PULSE = female pin header, 3 pins [form="♀ (female)"]

nets (from the pcb view):
  N1: RESET.1, TrimPot.leg2, NANO.GND, BATT.pin2, INK1.connector1, C1.2, R1.Pin_1, PULSE1.pin3, PULSE.pin3
  N2: RESET.3, NANO.RESET
  N3: TrimPot.leg1, NANO.3V3
  N4: TrimPot.wiper, INK1.connector7
  N5: NANO.D2, INK1.connector2
  N6: NANO.D3, INK1.connector3
  N7: NANO.D4, INK1.connector4
  N8: NANO.D5, INK1.connector5
  N9: NANO.D6, INK1.connector6
  N10: NANO.D9, LED_BLINK.pin1
  N11: NANO.VIN, SW1.connector1, C1.1
  N12: NANO.5V, INK1.connector0, PULSE1.pin2, PULSE.pin2
  N13: NANO.A0, PULSE1.pin1, PULSE.pin1
  N14: BATT.pin1, SW1.connector0
  N15: LED_BLINK.pin2, R1.Pin_0

notes:
  EKG 1, Pulse Monitor, 0
  For Pulse Conc
  Finger
