# Fritzing sketch id194_7_Segment_Display (saved by Fritzing 0.6.4b)
breadboards: 1

parts:
  Arduino1 = Arduino
  7_Segment1 = 7-Segment LED Display [package=THT]
  R1 = Resistor [tolerance=±5% resistance=220 package=THT]
  R2 = Resistor [tolerance=±5% resistance=220 package=THT]
  R3 = Resistor [tolerance=±5% resistance=220 package=THT]
  R4 = Resistor [tolerance=±5% resistance=220 package=THT]
  R5 = Resistor [tolerance=±5% resistance=220 package=THT]
  R6 = Resistor [tolerance=±5% resistance=220 package=THT]
  R7 = Resistor [tolerance=±5% resistance=220 package=THT]

nets:
  N1: Arduino1.D8, R3.Pin_1
  N2: Arduino1.D7, R5.Pin_1
  N3: Arduino1.D6, R4.Pin_1
  N4: Arduino1.D5, R7.Pin_1
  N5: Arduino1.D4, R1.Pin_1
  N6: Arduino1.D3, R2.Pin_1
  N7: Arduino1.D2, R6.Pin_1
  N8: Arduino1.GND, 7_Segment1.commAnode#7, R1.Pin_0
  N9: 7_Segment1.cathodeE, R4.Pin_0
  N10: 7_Segment1.cathodeD, R5.Pin_0
  N11: 7_Segment1.cathodeC, R3.Pin_0
  N12: 7_Segment1.cathodeB, R7.Pin_0
  N13: 7_Segment1.cathodeF, R2.Pin_0
  N14: 7_Segment1.cathodeG, R6.Pin_0
