# Fritzing sketch id194_8x8_RGB_Matrix_Driver_0 (saved by Fritzing 0.8.3b)
circuit board: 5.5cm x 5.2cm
circuit board: 5.5cm x 5.2cm
breadboards: 1

parts:
  Top = female pin header, 16 pins [form="♀ (female)"]
  Bottom = female pin header, 16 pins [form="♀ (female)"]
  74HC3595 = 74HC595 [chip_label=74HC595N]
  74HC4595 = 74HC595 [chip_label=74HC595N]
  J3 = molex pin header, 5 pins [form=molex]
  R19 = Resistor [tolerance=±5% resistance=220 package=THT]
  R20 = Resistor [tolerance=±5% resistance=220 package=THT]
  R21 = Resistor [tolerance=±5% resistance=220 package=THT]
  R22 = Resistor [tolerance=±5% resistance=220 package=THT]
  R23 = Resistor [tolerance=±5% resistance=220 package=THT]
  R24 = Resistor [tolerance=±5% resistance=220 package=THT]
  R25 = Resistor [tolerance=±5% resistance=220 package=THT]
  R26 = Resistor [tolerance=±5% resistance=220 package=THT]
  R27 = Resistor [tolerance=±5% resistance=220 package=THT]
  R28 = Resistor [tolerance=±5% resistance=220 package=THT]
  R29 = Resistor [tolerance=±5% resistance=220 package=THT]
  R30 = Resistor [tolerance=±5% resistance=220 package=THT]
  R31 = Resistor [tolerance=±5% resistance=220 package=THT]
  R32 = Resistor [tolerance=±5% resistance=220 package=THT]
  R33 = Resistor [tolerance=±5% resistance=220 package=THT]
  J4 = female pin header, 16 pins [form="♀ (female)"]
  R18 = Resistor [tolerance=±5% resistance=220 package=THT]
  R34 = Resistor [tolerance=±5% resistance=220 package=THT]
  R35 = Resistor [tolerance=±5% resistance=220 package=THT]
  R38 = Resistor [tolerance=±5% resistance=220 package=THT]
  R39 = Resistor [tolerance=±5% resistance=220 package=THT]
  R40 = Resistor [tolerance=±5% resistance=220 package=THT]
  R41 = Resistor [tolerance=±5% resistance=220 package=THT]
  J6 = female pin header, 16 pins [form="♀ (female)"]
  J7 = female pin header, 16 pins [form="♀ (female)"]
  74HC4596 = 74HC595 [chip_label=74HC595N]
  74HC4597 = 74HC595 [chip_label=74HC595N]
  R37 = Resistor [tolerance=±5% resistance=220 package=THT]
  R36 = Resistor [tolerance=±5% resistance=220 package=THT]
  J5 = female pin header, 16 pins [form="♀ (female)"]

nets:
  N1: Top.pin1, R18.Pin_0
  N2: Top.pin2, R20.Pin_0
  N3: Top.pin3, R21.Pin_0
  N4: Top.pin4, R22.Pin_0
  N5: Top.pin5, R23.Pin_0
  N6: Top.pin6, R24.Pin_0
  N7: Top.pin7, R25.Pin_0
  N8: Top.pin8, R26.Pin_0
  N9: Top.pin9, R19.Pin_0
  N10: Top.pin10, R27.Pin_0
  N11: Top.pin11, R28.Pin_0
  N12: Top.pin12, R29.Pin_0
  N13: Top.pin13, R30.Pin_0
  N14: Top.pin14, R31.Pin_0
  N15: Top.pin15, R32.Pin_0
  N16: Top.pin16, R33.Pin_0
  N17: Bottom.pin1, R34.Pin_1
  N18: Bottom.pin2, R35.Pin_1
  N19: Bottom.pin3, R36.Pin_1
  N20: Bottom.pin4, R37.Pin_1
  N21: Bottom.pin5, J5.pin1
  N22: Bottom.pin6, J5.pin2
  N23: Bottom.pin7, J5.pin3
  N24: Bottom.pin8, J5.pin4
  N25: Bottom.pin9, J5.pin5
  N26: Bottom.pin10, J5.pin6
  N27: Bottom.pin11, J5.pin7
  N28: Bottom.pin12, J5.pin8
  N29: Bottom.pin13, R38.Pin_1
  N30: Bottom.pin14, R39.Pin_1
  N31: Bottom.pin15, R40.Pin_1
  N32: Bottom.pin16, R41.Pin_1
  N33: 74HC3595.connector0, J6.pin15
  N34: 74HC3595.connector1, J6.pin14
  N35: 74HC3595.connector2, J6.pin13
  N36: 74HC3595.connector3, J6.pin12
  N37: 74HC3595.connector4, J6.pin11
  N38: 74HC3595.connector5, J6.pin10
  N39: 74HC3595.connector6, J6.pin9
  N40: 74HC3595.connector7, 74HC4595.connector7, J3.pin5, 74HC4596.connector7, 74HC4597.connector7
  N41: 74HC3595.connector8, 74HC4595.connector13
  N42: 74HC3595.connector9, 74HC3595.connector15, 74HC4595.connector9, 74HC4595.connector15, J3.pin1, 74HC4596.connector9, 74HC4596.connector15, 74HC4597.connector9, 74HC4597.connector15
  N43: 74HC3595.connector10, 74HC4595.connector10, J3.pin4, 74HC4596.connector10, 74HC4597.connector10
  N44: 74HC3595.connector12, 74HC4595.connector12, J3.pin3, 74HC4596.connector12, 74HC4597.connector12
  N45: 74HC3595.connector13, J3.pin2
  N46: 74HC3595.connector14, J6.pin16
  N47: 74HC4595.connector0, J6.pin7
  N48: 74HC4595.connector1, J6.pin6
  N49: 74HC4595.connector2, J6.pin5
  N50: 74HC4595.connector3, J6.pin4
  N51: 74HC4595.connector4, J6.pin3
  N52: 74HC4595.connector5, J6.pin2
  N53: 74HC4595.connector6, J6.pin1
  N54: 74HC4595.connector8, 74HC4596.connector13
  N55: 74HC4595.connector14, J6.pin8
  N56: R19.Pin_1, J4.pin9
  N57: R20.Pin_1, J4.pin2
  N58: R21.Pin_1, J4.pin3
  N59: R22.Pin_1, J4.pin4
  N60: R23.Pin_1, J4.pin5
  N61: R24.Pin_1, J4.pin6
  N62: R25.Pin_1, J4.pin7
  N63: R26.Pin_1, J4.pin8
  N64: R27.Pin_1, J4.pin10
  N65: R28.Pin_1, J4.pin11
  N66: R29.Pin_1, J4.pin12
  N67: R30.Pin_1, J4.pin13
  N68: R31.Pin_1, J4.pin14
  N69: R32.Pin_1, J4.pin15
  N70: R33.Pin_1, J4.pin16
  N71: J4.pin1, R18.Pin_1
  N72: R34.Pin_0, J5.pin9
  N73: R35.Pin_0, J5.pin10
  N74: R38.Pin_0, J5.pin13
  N75: R39.Pin_0, J5.pin14
  N76: R40.Pin_0, J5.pin15
  N77: R41.Pin_0, J5.pin16
  N78: J7.pin1, 74HC4597.connector14
  N79: J7.pin2, 74HC4597.connector0
  N80: J7.pin3, 74HC4597.connector1
  N81: J7.pin4, 74HC4597.connector2
  N82: J7.pin5, 74HC4597.connector3
  N83: J7.pin6, 74HC4597.connector4
  N84: J7.pin7, 74HC4597.connector5
  N85: J7.pin8, 74HC4597.connector6
  N86: J7.pin9, 74HC4596.connector14
  N87: J7.pin10, 74HC4596.connector0
  N88: J7.pin11, 74HC4596.connector1
  N89: J7.pin12, 74HC4596.connector2
  N90: J7.pin13, 74HC4596.connector3
  N91: J7.pin14, 74HC4596.connector4
  N92: J7.pin15, 74HC4596.connector5
  N93: J7.pin16, 74HC4596.connector6
  N94: 74HC4596.connector8, 74HC4597.connector13
  N95: R37.Pin_0, J5.pin12
  N96: R36.Pin_0, J5.pin11

notes:
  By coman3
  8x8 RGB M' Driver B1
  8x8 RGB M' Driver B2
  X
  O
