# Fritzing sketch id1951_Circuit_scheme_Heart_rate_monitor_theme_1_0 (saved by Fritzing 0.7.1b)
breadboards: 1

parts:
  Arduino1 = Arduino
  LED1 = LED - 5mm [color="Red (633nm)" package="5 mm [THT]"]
  R1 = Resistor [tolerance=±5% resistance=220 package=THT]
  LED2 = LED - 5mm [color="Red (633nm)" package="5 mm [THT]"]
  J1 = Piezo Speaker
  S1 = Pushbutton [package="[THT]"]
  R2 = Trimmer Potentiometer [maximum_resistance=10kΩ package=THT]
  LCD1 = LCD screen
  R3 = Resistor [tolerance=±5% resistance=220 package=THT]
  R4 = Resistor [tolerance=±5% resistance=220 package=THT]
  R5 = Photocell (LDR) [package=THT]
  S2 = Toggle Switch [package=THT]  # not connected
  S3 = Toggle Switch [package=THT]  # not connected
  Q1 = NPN-Transistor [package="TO92 [THT]"]

nets (from the breadboard view):
  N1: Arduino1.D12, LED2.cathode, J1.pin2
  N2: Arduino1.D8, R5.pin_1
  N3: Arduino1.D2, S1.Pin_3, S1.Pin_4, R3.Pin_1
  N4: Arduino1.D1TX, LCD1.DB7
  N5: Arduino1.+5V, LED1.anode, R1.Pin_0, LED2.anode, S1.Pin_1, S1.Pin_2, LCD1.LED+, R4.Pin_0, Q1.B
  N6: Arduino1.GND, R2.leg1, R2.leg2, LCD1.LED-, R3.Pin_0, Q1.C
  N7: Arduino1.A0, R1.Pin_1, R5.pin_0
  N8: Arduino1.A1, Q1.E
