# Fritzing sketch id1952_Heating_system_0 (saved by Fritzing 0.9.3b)
breadboards: 1

parts:
  R2_=_Potmeter = Trimmer Potentiometer [maximum_resistance=10kΩ package=THT]
  OPAMP = LM393 [package=so08]
  N-FET = MOSFET-NCHANNEL [package=to220v]
  R3_=_220_Ohms = Resistor [tolerance=±5% resistance=220 package="2512 [SMD]"]
  Red_LED = smd LED [color="Red (633nm)" package="0805 [SMD]"]
  Power_souce_5V = DC Power [voltage=5]
  R1 = Temperature Sensor (Thermistor) [thermistor_type=NTC package=THT]
  R1_=_4_7k_Ohms = Resistor [tolerance=±5% resistance=220 package="2512 [SMD]"]
  Heating_element = Resistor [tolerance=±5% resistance=220 package="1206 [SMD]"]

nets:
  N1: R2_=_Potmeter.leg1, N-FET.S, Red_LED.cathode, Power_souce_5V.V-, R1_=_4_7k_Ohms.Pin_1
  N2: R2_=_Potmeter.wiper, OPAMP.G1_+IN
  N3: R2_=_Potmeter.leg2, OPAMP.G1_V+, Power_souce_5V.V+, R1.pin_1, Heating_element.Pin_0
  N4: OPAMP.G1_OUT, N-FET.G, R3_=_220_Ohms.Pin_0
  N5: OPAMP.G1_-IN, R1.pin_0, R1_=_4_7k_Ohms.Pin_0
  N6: N-FET.D, Heating_element.Pin_1
  N7: R3_=_220_Ohms.Pin_1, Red_LED.anode
