# Fritzing sketch id1953_helloworld_0 (saved by Fritzing 0.9.1b)
breadboards: 1

parts:
  XTAL1 = Crystal [frequency="16 Mhz" package=THT]  # not connected
  Y1 = Resonator [frequency="16 Mhz" package=THT]  # not connected
  パーツ1 = Arduino Nano (Rev3.0)
  D1 = Rectifier Diode [part_number=1N4001 package="300 mil [THT]"]  # not connected
  LED1 = LED - 5mm [color="Red (633nm)" package="5 mm [THT]"]
  R1 = Resistor [tolerance=±5% resistance=220 package=THT]  # not connected
  Q1 = PNP-Transistor [package="TO92 [THT]"]  # not connected
  C2 = Ceramic Capacitor [capacitance=100nF package="100 mil [THT, multilayer]"]  # not connected
  L1 = Inductor [package="400 mil [THT]"]  # not connected
  R2 = Trimmer Potentiometer [maximum_resistance=10kΩ package=THT]
  R4 = Photocell (LDR) [package=THT]  # not connected
  S2 = Reed switch [package=THT]
  S3 = Tilt Switch [package=THT]  # not connected
  LED2 = RGB LED (com. cathode, rgb) [package="5 mm [THT]"]  # not connected
  S4 = Round Pushbutton
  R5 = Resistor [tolerance=±5% resistance=220 package=THT]  # not connected
  L2 = Solenoid

nets:
  N1: パーツ1.GND, LED1.cathode, S4.leg1, L2.pin1
  N2: パーツ1.D2, LED1.anode
  N3: パーツ1.VIN, S2.pin_1
  N4: R2.wiper, S2.pin_2, S4.leg0, L2.pin2
