# Fritzing sketch id1954_cholo (saved by Fritzing 0.7.4b)
breadboards: 1

parts:
  Arduino1 = Arduino
  IC1 = L293D [package=THT]
  J1 = female pin header, 2 pins [form="♀ (female)"]
  J2 = female pin header, 2 pins [form="♀ (female)"]
  J4 = female pin header, 2 pins [form="♀ (female)"]
  J5 = female pin header, 2 pins [form="♀ (female)"]
  M1 = DC Motor
  M2 = DC Motor
  J7 = female pin header, 2 pins [form="♀ (female)"]
  J8 = female pin header, 2 pins [form="♀ (female)"]

nets:
  N1: Arduino1.GND, IC1.0V, J1.pin2, J2.pin1, J4.pin1, J4.pin2, J5.pin1, J5.pin2
  N2: Arduino1.D8, IC1.In_4
  N3: Arduino1.D7, IC1.In_3
  N4: Arduino1.D6, IC1.Enable_2
  N5: Arduino1.D5, IC1.Enable_1
  N6: Arduino1.D4, IC1.In_1
  N7: Arduino1.D3, IC1.In_2
  N8: Arduino1.+5V, IC1.+V, J7.pin1, J7.pin2, J8.pin1, J8.pin2
  N9: Arduino1.VIN, IC1.+Vmotor, J1.pin1, J2.pin2
  N10: IC1.Out_1_(_Controlled_by_Enable_1_), M2.pin_1
  N11: IC1.Out_2_(_Controlled_by_Enable_1_), M2.pin_2
  N12: IC1.Out_3_(_Controlled_by_Enable_2_), M1.pin_1
  N13: IC1.Out_4_(_Controlled_by_Enable_2_), M1.pin_2
