# Fritzing sketch id1954_hexapod_schematic_0 (saved by Fritzing 0.9.3b)
breadboards: 1

parts:
  J1 = Basic Servo
  J2 = Basic Servo
  J3 = Basic Servo
  J4 = Basic Servo
  J5 = Basic Servo
  J6 = Basic Servo
  J7 = Basic Servo
  J8 = Basic Servo
  J9 = Basic Servo
  J10 = Basic Servo
  J11 = Basic Servo
  J12 = Basic Servo
  Part1 = Arduino Mega 2560 (Rev3)

nets:
  GND: J1.gnd, J2.gnd, J3.gnd, J4.gnd, J5.gnd, J6.gnd, J7.gnd, J8.gnd, J9.gnd, J10.gnd, J11.gnd, J12.gnd, Part1.GND
  VCC: J1.vcc, J2.vcc, J3.vcc, J4.vcc, J5.vcc, J6.vcc, J7.vcc, J8.vcc, J9.vcc, J10.vcc, J11.vcc, J12.vcc
  N1: J1.pulse, J5.pulse, J10.pulse, Part1.D10_PWM
  N2: J2.pulse, J6.pulse, J9.pulse, Part1.D11_PWM
  N3: J3.pulse, J8.pulse, J12.pulse, Part1.D8_PWM
  N4: J4.pulse, J7.pulse, J11.pulse, Part1.D9_PWM
