# Fritzing sketch id1956_Untitled_Sketch_0 (saved by Fritzing 0.9.3b)
breadboards: 1

parts:
  C1 = Tantalum Capacitor [capacitance=1μF package="100 mil [THT, tantalum]"]
  C2 = Tantalum Capacitor [capacitance=1μF package="100 mil [THT, tantalum]"]
  C3 = Tantalum Capacitor [capacitance=1μF package="100 mil [THT, tantalum]"]
  R1 = Resistor [tolerance=±5% resistance=220 package=THT]
  R2 = Resistor [tolerance=±5% resistance=220 package=THT]
  U1 = Barometric Pressure Sensor  # not connected
  Componente1 = Arduino Pro  # not connected

nets:
  N1: C1.+, R2.Pin_0
  N2: C2.-, R2.Pin_1
  N3: C2.+, R1.Pin_0
  N4: C3.-, R1.Pin_1
