# Fritzing sketch id1957_Arduino_Flexiforce_0 (saved by Fritzing 0.9.3b)
breadboards: 1

parts:
  Part1 = Arduino Uno (Rev3)
  U1 = LM 358 Dual Op-Amp [package="DIP8 [THT]"]
  R3 = TRIMPOT [package=trimpot_pth_s3_lock]
  J4 = Basic Force Sensing Resistor (FSR) [package=THT]
  R4 = Resistor [tolerance=±5% resistance=6.8k package="0603 [SMD]"]
  R5 = Resistor [tolerance=±5% resistance=22k package="0603 [SMD]"]
  R6 = Resistor [tolerance=±5% resistance=470 package="0603 [SMD]"]
  R7 = Resistor [tolerance=±5% resistance=4.7k package="0603 [SMD]"]
  R8 = Resistor [tolerance=±5% resistance=220 package="0603 [SMD]"]
  LED1 = LED - 3mm [color="Red (633nm)" package="3 mm [THT]"]

nets:
  N1: Part1.A0, U1.connector5, R5.Pin_0
  N2: Part1.D9_PWM, R8.Pin_1
  N3: Part1.GND, U1.connector3, J4.pin_1, R4.Pin_0, R6.Pin_1, LED1.cathode
  N4: Part1.5V, U1.connector6, R7.Pin_1
  N5: U1.connector1, R3.WIPER, R3.CW, J4.pin_0
  N6: R6.Pin_0, R7.Pin_0
