# Fritzing sketch id1958_l293d_0 (saved by Fritzing 0.9.2b)
breadboards: 1

parts:
  IC1 = L293D [package=THT]  # not connected
  Q1 = MOSFET-NCHANNEL [package=to220v]
  Q2 = Basic FET P-Channel [package="DPak [SMD]"]
  Q3 = MOSFET-NCHANNEL [package=to220v]
  Q4 = Basic FET P-Channel [package="DPak [SMD]"]
  Part1 = Arduino Uno (Rev3)  # not connected
  M1 = DC Motor  # not connected
  U1 = LIPO-2000mAh [package=lipo-2000]  # not connected

nets:
  N1: Q1.G, Q2.Gate
  N2: Q1.D, Q2.drain
  N3: Q1.S, Q3.S
  N4: Q2.source, Q4.source
  N5: Q3.G, Q4.Gate
  N6: Q3.D, Q4.drain
