# Fritzing sketch id1959_rgb_def_0 (saved by Fritzing 0.7.1b)
breadboards: 1

parts:
  Componente1 = Arduino_Pro_Mini_3.3V
  Q2 = NPN-Transistor [part_number=BC337 package="TO92 [THT]"]
  Q3 = NPN-Transistor [part_number=BC337 package="TO92 [THT]"]
  R1 = Resistor [tolerance=±5% resistance=1k package=THT]
  R2 = Resistor [tolerance=±5% resistance=1k package=THT]
  R3 = Resistor [tolerance=±5% resistance=1k package=THT]
  RGBout = female pin header, 4 pins [form="♀ (female)"]
  DC_12V = Power plug
  D1 = Rectifier Diode [part_number=1N4001 package="300 mil [THT]"]
  R4 = Rotary Potentiometer (Small) [maximum_resistance=10kΩ]
  R5 = Rotary Potentiometer (Small) [maximum_resistance=10kΩ]
  SW1 = female pin header, 2 pins [form="♀ (female)"]
  R6 = Resistor [tolerance=±5% resistance=10k package=THT]
  R7 = Resistor [tolerance=±5% resistance=10k package=THT]
  SW2 = Toggle Switch [package=THT]
  Q1 = NPN-Transistor [part_number=BC337 package="TO92 [THT]"]
  J2 = female pin header, 4 pins [form="♀ (female)"]

nets:
  N1: Componente1.connector22, D1.cathode
  GND: Componente1.connector23, Q2.E, Q3.E, DC_12V.GND, R4.leg1, R5.leg1, R6.Pin_1, R7.Pin_1, Q1.E
  5V: Componente1.connector25, R4.leg2, R5.leg2, SW2.COM
  N2: Componente1.connector28, R5.wiper
  N3: Componente1.connector29, R4.wiper
  N4: Componente1.connector32, R6.Pin_0, SW2.L1
  N5: Componente1.connector33, R7.Pin_0, SW2.L2
  N6: Componente1.connector37, R1.Pin_0
  N7: Componente1.connector38, R3.Pin_1
  N8: Componente1.connector40, R2.Pin_0
  N9: Q2.B, R3.Pin_0
  N10: Q2.C, RGBout.pin3, J2.pin3
  N11: Q3.B, R2.Pin_1
  N12: Q3.C, RGBout.pin2, J2.pin2
  N13: R1.Pin_1, Q1.B
  N14: RGBout.pin1, D1.anode, SW1.pin2, J2.pin1
  N15: RGBout.pin4, Q1.C, J2.pin4
  N16: DC_12V.VCC, SW1.pin1

notes:
  by Toggio
  RGB Lamp 1.0
  Luca & Roby
  Arduino Pro Mini 5 V
