# Fritzing sketch id1960_Hilo_machine_circuit_0 (saved by Fritzing 0.9.3b)
breadboards: 1

parts:
  Motor = DC Motor
  Potentiometer = Basic FET N-Channel [package="TO220 [THT]"]
  Transistor = POT [package=pot_mammoth]
  VCC1 = Battery block 9V

nets:
  N1: Motor.pin_1, Potentiometer.gate
  N2: Motor.pin_2, VCC1.+
  N3: Potentiometer.drain, Transistor.S
  N4: Potentiometer.source, Transistor.A
  N5: Transistor.E, VCC1.-
