# Fritzing sketch id1961_HK592_0 (saved by Fritzing 0.9.0b)
circuit board: 2.2cm x 2.2cm
breadboards: 1

parts:
  Q1 = NPN-Transistor [package="TO92 [THT]"]
  U2 = WATB_HK592 [chip_label=HK592]
  SPKR1 = Loudspeaker
  VCC1 = Battery
  S1 = Pushbutton [package=THT]
  R1 = Resistor [tolerance=±5% resistance=100k package=THT]

nets:
  N1: Q1.E, SPKR1.pin1
  N2: Q1.B, R1.Pin_1
  N3: Q1.C, U2.connector0, VCC1.-
  N4: U2.connector1, S1.leg1
  N5: U2.connector2, SPKR1.pin2, VCC1.+, S1.leg0
  N6: U2.connector3, R1.Pin_0

notes:
  W.A. ten Brink
  Knowledge And Technology Joyfully Engaged
