# Fritzing sketch id1961_LDR_led (saved by Fritzing 0.5.2b)
breadboards: 1

parts:
  Arduino1 = Arduino
  R1 = Photocell (LDR) [package=THT]
  R2 = Resistor [resistance=1k package=THT]
  LED1 = Red LED - 5mm [package="5 mm [THT]"]
  R3 = Resistor [resistance=220 package=THT]

nets:
  N1: Arduino1.GND, R2.Pin_0, LED1.cathode
  N2: Arduino1.D13, R3.Pin_0
  N3: Arduino1.+5V, R1.pin_1
  N4: Arduino1.A0, R1.pin_0, R2.Pin_1
  N5: LED1.anode, R3.Pin_1
