# Fritzing sketch id1962_LDR_without_Arduino_with_V_reg_Case_1 (saved by Fritzing 0.5.2b)
breadboards: 1

parts:
  U1 = Voltage Regulator - 5V [package="TO220 [THT]"]
  S1 = Pushbutton [package=THT]
  C2 = Electrolytic Capacitor [capacitance=10µF rated_voltage=35V package="100 mil [THT, electrolytic]"]
  C1 = Electrolytic Capacitor [capacitance=100µF rated_voltage=35V package="200 mil [THT, electrolytic]"]
  R1 = Resistor [resistance=330 package=THT]
  LED1 = Red LED - 5mm [package="5 mm [THT]"]
  VCC1 = Battery block 9V
  D1 = Rectifier Diode [package="300 mil [THT]"]
  R2 = Temperature Sensor (Thermistor) [package=THT]
  LED1_2 = green LED - 5mm [package="5 mm [THT]"]
  R1_2 = Resistor [resistance=220 package=THT]
  R3 = Photocell (LDR) [package=THT]
  R1_3 = Resistor [resistance=1k package=THT]
  Q1 = NPN-Transistor [package="TO92 [THT]"]
  R1_4 = Resistor [resistance=10k package=THT]

nets:
  N1: U1.input_voltage, C1.+, R2.pin_1
  N2: U1.GND, C2.-, C1.-, R1.Pin_1, VCC1.-, Q1.C, R1_4.Pin_0
  N3: U1.output_voltage, C2.+, LED1.anode, R1_2.Pin_0, R3.pin_1
  N4: S1.leg0, D1.anode
  N5: S1.leg1, VCC1.+
  N6: R1.Pin_0, LED1.cathode
  N7: D1.cathode, R2.pin_0
  N8: LED1_2.cathode, Q1.E
  N9: LED1_2.anode, R1_2.Pin_1
  N10: R3.pin_0, R1_3.Pin_1, R1_4.Pin_1
  N11: R1_3.Pin_0, Q1.B
