# Fritzing sketch id1962_rgbLED_switch_0 (saved by Fritzing 0.9.2b)
breadboards: 1

parts:
  LED1 = RGB LED (com. cathode, rgb) [package="5 mm [THT]"]
  R1 = Resistor [tolerance=±5% resistance=220 package=THT]
  R2 = Resistor [tolerance=±5% resistance=220 package=THT]
  Onderdeel1 = Arduino Uno (Rev3)
  R3 = Resistor [tolerance=±5% resistance=220 package=THT]
  S1 = Pushbutton [package="[THT]"]
  R4 = Resistor [tolerance=±5% resistance=220 package=THT]

nets:
  N1: LED1.red_anode, R3.Pin_1
  N2: LED1.common_cathode, R2.Pin_1
  N3: LED1.green_anode, Onderdeel1.GND, R4.Pin_0
  N4: LED1.blue_anode, R1.Pin_0
  N5: R1.Pin_1, Onderdeel1.D8
  N6: R2.Pin_0, Onderdeel1.D9_PWM
  N7: Onderdeel1.D10_PWM/SS, R3.Pin_0
  N8: Onderdeel1.D4, S1.Pin_3, S1.Pin_4, R4.Pin_1
  N9: Onderdeel1.5V, S1.Pin_1, S1.Pin_2
