# Fritzing sketch id1964_esquema_sensor_led_speaker_0 (saved by Fritzing 0.9.0b)
breadboards: 1

parts:
  Arduino = Arduino Uno (Rev3) - ICSP
  S_Temp = TMP36 [package=to-92-kit]
  R1 = Resistor [tolerance=±5% resistance=560 package=THT]
  R2 = Resistor [tolerance=±5% resistance=560 package=THT]
  R3 = Resistor [tolerance=±5% resistance=560 package=THT]
  LED1 = RGB LED (com. cathode, rgb) [package="5 mm [THT]"]
  Speaker = Piezo Speaker

nets:
  N1: Arduino.A0, S_Temp.VOUT
  N2: Arduino.ICSP_MOSI, Arduino.D11_PWM/MOSI, R1.Pin_1
  N3: Arduino.D9_PWM, R3.Pin_1
  N4: Arduino.D10_PWM/SS, R2.Pin_1
  N5: Arduino.D12/MISO, Speaker.pin2
  5V: Arduino.5V, S_Temp.VCC
  GND: Arduino.GND, S_Temp.GND, LED1.common_cathode, Speaker.pin1
