# Fritzing sketch id1966_Hola_Mundo_BT_0 (saved by Fritzing 0.9.2b)

parts:
  Parte1 = Arduino Uno (Rev3)
  LED1 = smd LED [color="Red (633nm)" package="1206 [SMD]"]  # not connected
  Parte4 = bluetooth-module

nets:
  N1: Parte1.D0/RX, Parte4.connector15
  N2: Parte1.D1/TX, Parte4.connector16
  N3: Parte1.5V, Parte4.connector13
  N4: Parte1.GND, Parte4.connector14
