# Fritzing sketch id1969_noderev3_sdcard_rtc_spi_ext_0 (saved by Fritzing 0.8.5b)
circuit board: 6.4cm x 6.4cm
breadboards: 1

parts:
  RFM12B1 = rfm12b_dip_smdconn
  R1 = Resistor [tolerance=±5% resistance=4.7k package=THT]
  R3 = Resistor [tolerance=±5% resistance=4.7k package=THT]
  R4 = Resistor [tolerance=±5% resistance=10k package=THT]
  R5 = Resistor [tolerance=±5% resistance=10k package=THT]
  R6 = Resistor [tolerance=±5% resistance=10k package=THT]
  Arduino_micro = Arduino Micro (Rev3)
  C1 = Electrolytic Capacitor [capacitance=0.1µF package="100 mil [THT, electrolytic]"]
  C2 = Ceramic Capacitor [capacitance=10µF package="100 mil [THT, multilayer]"]
  F1 = Resettable Fuse PTC [package=ptc-1206]
  power = USB Connectors [package=usb-microb]
  Interface = RJ45 Jack [package=rj45-8]
  R2 = Resistor [tolerance=±5% resistance=4.7k package=THT]
  DHT22 = Humidity and Temperature Sensor RHT03
  Q1 = NPN-Transistor [package="TO92 [THT]"]
  Q2 = NPN-Transistor [package="TO92 [THT]"]
  R7 = Resistor [tolerance=±5% resistance=4.7k package=THT]
  R8 = Resistor [tolerance=±5% resistance=4.7k package=THT]
  R9 = Resistor [tolerance=±5% resistance=4.7k package=THT]
  J1 = female pin header, 3 pins [form="♀ (female)"]
  BHP085 = Barometric Pressure Sensor - BMP085 Breakout
  ANT1 = Antenna
  Antenna = Pad [width=2 height=2 connect=center]
  R10 = Resistor [tolerance=±5% resistance=4.7k package=THT]
  U1 = microSD Socket [package=usd-socket-pp]
  R12 = Resistor [tolerance=±5% resistance=4.7k package="1206 [SMD]"]
  R11 = Resistor [tolerance=±5% resistance=10k package="1206 [SMD]"]
  bat = female pin header, 2 pins [form="♀ (female)"]
  ds1307 = DS1307 [package=THT]
  Y1 = CRYSTAL [package=crystal-32khz-smd]
  RTCBAT = Header 2 [package=molex-1x2_lock]
  Ext_Board = female pin header, 7 pins [form="♀ (female)"]

nets:
  N1: RFM12B1.connector1, R2.Pin_0, U1.DI, Ext_Board.pin5
  N2: RFM12B1.connector2, R3.Pin_0
  N3: RFM12B1.connector3, Arduino_micro.D3/SCL
  GND: RFM12B1.connector6, R4.Pin_1, R5.Pin_1, R6.Pin_1, Arduino_micro.GND, C1.-, C2.0, power.GND, Interface.1, Interface.2, Interface.6, DHT22.GND_2, Q1.E, Q2.E, R9.Pin_0, J1.pin3, BHP085.GND, U1.GND, R11.Pin_1, bat.pin1, RTCBAT.1, Ext_Board.pin7
  N4: RFM12B1.connector9, Arduino_micro.MISO, U1.DO, Ext_Board.pin6
  N5: RFM12B1.connector10, R1.Pin_0, U1.SCK, Ext_Board.pin4
  VCC: RFM12B1.connector11, Arduino_micro.3V3, C1.+, C2.1, J1.pin1, BHP085.VCC, U1.VCC, ds1307.+V, Ext_Board.pin1
  N6: R1.Pin_1, R4.Pin_0, Arduino_micro.SCK
  N7: R3.Pin_1, R6.Pin_0, Arduino_micro.D10_PWM/A10
  N8: R5.Pin_0, Arduino_micro.MOSI, R2.Pin_1
  N9: Arduino_micro.D2/SDA, DHT22.Data-signal, R10.Pin_0
  N10: Arduino_micro.D4_PWM/A6, R7.Pin_1
  N11: Arduino_micro.D5_PWM, R8.Pin_1
  N12: Arduino_micro.D6_PWM/A7, Interface.5, R9.Pin_1, J1.pin2
  N13: Arduino_micro.D8_PWM/A8, Ext_Board.pin2
  N14: Arduino_micro.D9_PWM/A9, Ext_Board.pin3
  N15: Arduino_micro.D12_PWM/A11, R12.Pin_0
  N16: Arduino_micro.VIN, F1.1
  5V: Arduino_micro.5V, Interface.7, Interface.8, DHT22.Vcc, R10.Pin_1
  N17: Arduino_micro.A5, BHP085.SCL, ds1307.SCL_-_I2C_Clock
  N18: Arduino_micro.A4, BHP085.SDA, ds1307.SDA_-_I2C_Data
  N19: F1.2, power.VBUS, bat.pin2
  N20: Interface.3, Q2.C
  N21: Interface.4, Q1.C
  GND_2: DHT22.GND_1
  N22: Q1.B, R8.Pin_0
  N23: Q2.B, R7.Pin_0
  N24: ANT1.antenna_lead, Antenna.pad
  N25: U1.CS, R12.Pin_1, R11.Pin_0
  N26: ds1307.X1_-_Crystal, Y1.1
  N27: ds1307.X2_-_Crystal, Y1.2
  N28: ds1307.Vbat_-_Backup_Supply, RTCBAT.2

notes:
  gnd
  sdo
  sdi
  sck
  i/o1
  i/o2
  vcc3
