# Fritzing sketch id1970_Home_Automation_0 (saved by Fritzing 0.9.2b)
circuit board: 8.46667cm x 5.64444cm
breadboards: 1

parts:
  Part1 = Arduino Uno (Rev3)  # not connected
  Part2 = Arduino Ethernet Shield (Rev3)
  LCD1 = LCD screen
  DHT1 = DHT11_Temperature_and_Humitidy_Sensor
  IR1 = TSOP312.., 314.. [package=THT]
  U1 = 2ChannelRelay
  PIR1 = PIR_sensor

nets:
  N1: Part2.D8, LCD1.DB7
  N2: Part2.PWM_D9, DHT1.connector2
  N3: Part2.A0, PIR1.connector2
  N4: Part2.A1, U1.connector2
  N5: Part2.A2, U1.connector3
  N6: Part2.A3, IR1.Data
  N7: Part2.D2, LCD1.RS
  N8: Part2.PWM_D3, LCD1.E
  N9: Part2.PWM_D5, LCD1.DB4
  N10: Part2.PWM_D6, LCD1.DB5
  N11: Part2.D7, LCD1.DB6
  5V: Part2.5V, LCD1.VDD, LCD1.LED+, DHT1.connector1, IR1.Vs, U1.connector0, PIR1.connector1
  GND: Part2.GND, LCD1.VSS, LCD1.V0, LCD1.R/W, LCD1.LED-, DHT1.connector4, IR1.GND, U1.connector1, PIR1.connector3
