# Fritzing sketch id1972_board_rd_0 (saved by Fritzing 0.9.2b)
circuit board: 5.9cm x 5.9cm
breadboards: 1

parts:
  Bauteil1 = Arduino Pro Mini v13
  U1 = RJ45 Jack [package=rj45-8]
  U2 = RJ45 Jack [package=rj45-8]
  J2 = female pin header, 8 pins [form="♀ (female)"]  # not connected
  J1 = female pin header, 8 pins [form="♀ (female)"]  # not connected
  J3 = female pin header, 4 pins [form="♀ (female)"]
  J4 = female pin header, 4 pins [form="♀ (female)"]
  U3 = MAX485 [package=dil08]
  Q1 = PNP-Transistor [package="TO92 [THT]"]
  R1 = Resistor [tolerance=±5% resistance=4.7k package=THT]
  J5 = screw terminal, 3 pins
  R2 = Resistor [tolerance=±5% resistance=10k package=THT]
  R3 = Resistor [tolerance=±5% resistance=220 package=THT]
  J6 = screw terminal, 3 pins
  J7 = screw terminal, 3 pins
  J8 = screw terminal, 3 pins
  R4 = Resistor [tolerance=±5% resistance=220 package=THT]
  R5 = Resistor [tolerance=±5% resistance=220 package=THT]

nets:
  N1: Bauteil1.D0/TX, U3.DI
  N2: Bauteil1.RAW, J4.pin1, U3.VCC, Q1.E, R1.Pin_1, J5.pin3, J6.pin1, J7.pin1, J8.pin1
  GND: Bauteil1.GND, J4.pin4, U3.GND, Q1.C, R2.Pin_1, R3.Pin_1, R4.Pin_0, R5.Pin_0
  N3: Bauteil1.D7, J8.pin3, R4.Pin_1
  N4: Bauteil1.D6_PWM, J7.pin3, R5.Pin_1
  N5: Bauteil1.D5_PWM, R3.Pin_0, J6.pin3
  N6: Bauteil1.D4, J5.pin1, R2.Pin_0
  N7: Bauteil1.D3_PWM, Q1.B, R1.Pin_0
  N8: Bauteil1.D2, U3.RE, U3.DE
  N9: Bauteil1.D1/RX, U3.RO
  N10: U1.4, U2.4, J3.pin1
  N11: U1.5, U2.5, J3.pin4
  N12: U1.7, U2.7, U3.A
  N13: U1.8, U2.8, U3.B

notes:
  lm2596
