# Fritzing sketch id1973_hc_05_relay_out2_mobile_control_0 (saved by Fritzing 0.9.2b)

parts:
  LED3 = custom_light_bulb
  LED17 = smd LED [color="Orange (620nm)" package="0603 [SMD]"]
  LED19 = smd LED [color="Blue (430nm)" package="0603 [SMD]"]  # not connected
  LED21 = smd LED [color="Green (555nm)" package="0603 [SMD]"]
  LED22 = smd LED [color="Yellow (595nm)" package="0603 [SMD]"]
  LED24 = smd LED [color="Red (633nm)" package="0603 [SMD]"]
  JY-MCU1 = Arduino Nano (Rev3.0)
  Part3 = Bluetooth HC-05 Macho
  R17 = Resistor [tolerance=±5% resistance=220 package=THT]
  R18 = Resistor [tolerance=±5% resistance=220 package=THT]
  R19 = Resistor [tolerance=±5% resistance=220 package=THT]
  R20 = Resistor [tolerance=±5% resistance=220 package=THT]
  R21 = Resistor [tolerance=±5% resistance=220 package=THT]
  Power_plug4 = Power plug
  R22 = Resistor [tolerance=±5% resistance=2.2k package=THT]
  R24 = Resistor [tolerance=±5% resistance=1k package=THT]
  Part4 = Lilypad Battery Connect
  U4 = SWITCH-SPST-2 [package=switch-spst-vertical]
  LED27 = custom_light_bulb
  Part5 = Lilypad Battery Connect
  Z1 = VARISTOR [package=0603-res]
  LED29 = smd LED [color="Orange (620nm)" package="0603 [SMD]"]  # not connected
  U3 = 4ChannelRelay
  R25 = Resistor [tolerance=±5% resistance=220 package=THT]

nets:
  N1: LED3.connector0, U3.connector11
  N2: LED17.cathode, LED21.cathode, LED22.cathode, LED24.cathode
  N3: JY-MCU1.D2, Part3.TXD
  N4: JY-MCU1.D3, R24.Pin_0
  N5: JY-MCU1.D4, R20.Pin_1
  N6: JY-MCU1.D5, R18.Pin_1
  N7: JY-MCU1.D6, R21.Pin_1
  N8: JY-MCU1.D7, R19.Pin_1
  N9: JY-MCU1.D8, R17.Pin_1
  N10: JY-MCU1.D9, U3.connector10
  N11: JY-MCU1.D10, U3.connector17
  N12: JY-MCU1.D12/MISO, U3.connector2
  N13: JY-MCU1.VIN, U4.P
  GND: JY-MCU1.GND, JY-MCU1.RESET, Part3.GND, R22.Pin_0, U3.connector1
  5V: JY-MCU1.5V, Part3.VCC, U3.connector0
  N14: JY-MCU1.D13/SCK, R25.Pin_1
  N15: Part3.RXD, R22.Pin_1
  N16: Power_plug4.VCC, U4.O
  N17: Part4.-, U3.connector12, U3.connector16
  N18: Part4.+, U3.connector14
  N19: LED27.connector0, U3.connector4
  N20: Part5.-, U3.connector5, U3.connector9
  N21: Part5.+, U3.connector7
  N22: Z1.1, Z1.2

notes:
  220V AC power supply
  input
  5-12 DC IN
  S2
  Hand held Switch
  10A
  220 AC
  relay1
  relay2
  relay3
  relay4
  VCC
  D9
  D10
  D11
  D12
  GND
  ON / OFF
  Arduino
  S1
  Hand held Switch
  Load2
  Load1
  D8 D7 D6 D5 D4 D13
  D8=Load1
  D7=Load2
  D6=All control
  D5=Mode 0
  handheld mode
  D4=Mode 1
  mobile mode
  D13=No opration
  other switch mobile App
  D9&D11=Switch ON/OFF Load1,2
  D12&D10=Mode Changing
