# Fritzing sketch id1974_Prototype_Home_Security_0 (saved by Fritzing 0.9.3b)
breadboards: 1

parts:
  Part1 = Arduino Mega 2560 (Rev3)
  LCD1 = LCD screen
  R1 = Resistor [tolerance=±5% resistance=220 package="2010 [SMD]"]
  R2 = Resistor [tolerance=±5% resistance=10 package="2010 [SMD]"]
  LED1 = RGB LED (com. anode, rbg) [package="5 mm [THT]"]
  R3 = Resistor [tolerance=±5% resistance=220 package="2010 [SMD]"]
  R4 = Resistor [tolerance=±5% resistance=220 package="2010 [SMD]"]
  R5 = Resistor [tolerance=±5% resistance=220 package="2010 [SMD]"]
  J1 = Piezo Speaker
  R6 = Resistor [tolerance=±5% resistance=220 package="2010 [SMD]"]
  hc-sr1 = hc-sr04
  J2 = Basic Servo
  Matrix_keypad1 = CMG

nets:
  N1: Part1.D20/SDA, R3.Pin_1
  N2: Part1.D19/RX1, R5.Pin_1
  N3: Part1.D18/TX1, R4.Pin_1
  N4: Part1.D13_PWM, J1.pin2
  N5: Part1.D12_PWM, LCD1.RS
  N6: Part1.D11_PWM, LCD1.E
  N7: Part1.D9_PWM, Matrix_keypad1.connector32
  N8: Part1.D8_PWM, Matrix_keypad1.connector31
  VCC: Part1.5V, LCD1.VDD, LCD1.LED-, hc-sr1.VCC, J2.vcc
  GND: Part1.GND, LCD1.VSS, LCD1.R/W, R1.Pin_1, R2.Pin_1, LED1.common_anode, R6.Pin_1, hc-sr1.GND, J2.gnd
  N9: Part1.D2_PWM, Matrix_keypad1.connector25
  N10: Part1.D3_PWM, Matrix_keypad1.connector26
  N11: Part1.D4_PWM, Matrix_keypad1.connector27
  N12: Part1.D5_PWM, Matrix_keypad1.connector28
  N13: Part1.D6_PWM, Matrix_keypad1.connector29
  N14: Part1.D7_PWM, Matrix_keypad1.connector30
  N15: Part1.D22, LCD1.DB7
  N16: Part1.D24, LCD1.DB6
  N17: Part1.D26, LCD1.DB5
  N18: Part1.D28, LCD1.DB4
  N19: Part1.D30, J2.pulse
  N20: Part1.D32, hc-sr1.Echo
  N21: Part1.D34, hc-sr1.Trig
  N22: LCD1.LED+, R1.Pin_0
  N23: LED1.red_cathode, R3.Pin_0
  N24: LED1.blue_cathode, R5.Pin_0
  N25: LED1.green_cathode, R4.Pin_0
  N26: J1.pin1, R6.Pin_0
