# Fritzing sketch id1975_qqqqq_0 (saved by Fritzing 0.8.7b)
breadboards: 2

parts:
  Matrix_keypad1 = CMG
  Arduino_Mega_2500 = Arduino Mega 2560 (Rev3)
  lock = LED - 3mm [color="Red (633nm)" package="3 mm [THT]"]
  R1 = Resistor [tolerance=±5% resistance=100 package=THT]
  Unlock = LED - 3mm [color="Green (555nm)" package="3 mm [THT]"]
  R2 = Resistor [tolerance=±5% resistance=100 package=THT]
  light_back = LED - 3mm [color="Yellow (585nm)" package="3 mm [THT]"]
  light_front = LED - 3mm [color="Yellow (585nm)" package="3 mm [THT]"]
  R3 = Resistor [tolerance=±5% resistance=100 package=THT]
  R4 = Resistor [tolerance=±5% resistance=100 package=THT]
  Servo_Door = Basic Servo
  Servo_Camera = Basic Servo
  VCC2 = Battery
  Buzzer = Piezo Speaker
  R5 = Resistor [tolerance=±5% resistance=100 package=THT]
  Flame_sensor = Humidity and Temperature Sensor RHT03
  LEC_warning = LED - 3mm [color="Red (633nm)" package="3 mm [THT]"]
  R6 = Resistor [tolerance=±5% resistance=100 package=THT]
  magnetic_switch = SWITCH-MOMENTARY-2 [package=tactile-switch-1101ne]
  magnetic_switch2 = SWITCH-MOMENTARY-2 [package=tactile-switch-1101ne]

nets:
  N1: Matrix_keypad1.connector25, Arduino_Mega_2500.D53
  N2: Matrix_keypad1.connector26, Arduino_Mega_2500.D52
  N3: Matrix_keypad1.connector27, Arduino_Mega_2500.D51
  N4: Matrix_keypad1.connector28, Arduino_Mega_2500.D50
  N5: Matrix_keypad1.connector29, Arduino_Mega_2500.D49
  N6: Matrix_keypad1.connector30, Arduino_Mega_2500.D48
  N7: Matrix_keypad1.connector31, Arduino_Mega_2500.D47
  N8: Matrix_keypad1.connector32, Arduino_Mega_2500.D46
  N9: Arduino_Mega_2500.D10_PWM, R5.Pin_0
  N10: Arduino_Mega_2500.D9_PWM, R1.Pin_1
  N11: Arduino_Mega_2500.D8_PWM, R2.Pin_1
  N12: Arduino_Mega_2500.5V, Flame_sensor.GND_2
  GND: Arduino_Mega_2500.GND, lock.anode, Unlock.anode, light_back.anode, light_front.anode, Servo_Door.gnd, Servo_Camera.gnd, VCC2.-, Buzzer.pin1, Flame_sensor.GND_1, LEC_warning.anode, magnetic_switch.2, magnetic_switch2.2
  N13: Arduino_Mega_2500.D3_PWM, Flame_sensor.Data-signal
  N14: Arduino_Mega_2500.D5_PWM, R6.Pin_1
  N15: Arduino_Mega_2500.D6_PWM, R3.Pin_1
  N16: Arduino_Mega_2500.D7_PWM, R4.Pin_1
  N17: Arduino_Mega_2500.D24, Servo_Camera.pulse
  N18: Arduino_Mega_2500.D26, Servo_Door.pulse
  N19: Arduino_Mega_2500.D30, magnetic_switch.1
  N20: Arduino_Mega_2500.D32, magnetic_switch2.1
  N21: lock.cathode, R1.Pin_0
  N22: Unlock.cathode, R2.Pin_0
  N23: light_back.cathode, R3.Pin_0
  N24: light_front.cathode, R4.Pin_0
  VCC: Servo_Door.vcc, Servo_Camera.vcc, VCC2.+
  N25: Buzzer.pin2, R5.Pin_1
  N26: LEC_warning.cathode, R6.Pin_0
