# Fritzing sketch id1977_HomeDuino_Lite_1_0 (saved by Fritzing 0.8.5b)
circuit board: 6.88566cm x 5.36311cm

parts:
  ATMEGA328P-PU2 = atmega328 [package=dip]
  J1 = female pin header, 2 pins [form="♀ (female)"]
  J3 = female pin header, 2 pins [form="♀ (female)"]
  J4 = female pin header, 6 pins [form="♀ (female)"]
  J5 = female pin header, 8 pins [form="♀ (female)"]
  J6 = female pin header, 8 pins [form="♀ (female)"]
  Y1 = Resonator [frequency="16 Mhz" package=THT]
  J2 = female pin header, 2 pins [form="♀ (female)"]

nets:
  N1: ATMEGA328P-PU2.RESET, ATMEGA328P-PU2.VCC, ATMEGA328P-PU2.AVCC, ATMEGA328P-PU2.AREF, J3.pin1, J2.pin1
  N2: ATMEGA328P-PU2.D0_(RX), J1.pin1, J5.pin1
  N3: ATMEGA328P-PU2.D1_(TX), J1.pin2, J5.pin2
  N4: ATMEGA328P-PU2.D2, J5.pin3
  N5: ATMEGA328P-PU2.D3_(PWM), J5.pin4
  N6: ATMEGA328P-PU2.D4, J5.pin5
  GND: ATMEGA328P-PU2.GND, J3.pin2, Y1.GND, J2.pin2
  N7: ATMEGA328P-PU2.XLAT1, Y1.0
  N8: ATMEGA328P-PU2.XLAT2, Y1.pin_1
  N9: ATMEGA328P-PU2.D5_(PWM), J5.pin6
  N10: ATMEGA328P-PU2.D6_(PWM), J5.pin7
  N11: ATMEGA328P-PU2.D7, J5.pin8
  N12: ATMEGA328P-PU2.D8, J6.pin1
  N13: ATMEGA328P-PU2.D9_(PWM), J6.pin2
  N14: ATMEGA328P-PU2.D10_(PWM), J6.pin3
  N15: ATMEGA328P-PU2.D11_(PWM), J6.pin4
  N16: ATMEGA328P-PU2.D12, J6.pin5
  N17: ATMEGA328P-PU2.D13, J6.pin6
  N18: ATMEGA328P-PU2.A0, J4.pin6
  N19: ATMEGA328P-PU2.A1, J4.pin5
  N20: ATMEGA328P-PU2.A2, J4.pin4
  N21: ATMEGA328P-PU2.A3, J4.pin3
  N22: ATMEGA328P-PU2.A4, J4.pin2
  N23: ATMEGA328P-PU2.A5, J4.pin1

notes:
  13 12 11 10 9 8
  7  6 5  4 3  2  1  0
  A0 A1 A2 A3 A4 A5
  RX TX
  - +
  HomeDuino Lite
