# Fritzing sketch id197_test01_0 (saved by Fritzing 0.9.3b)
breadboards: 1

parts:
  LED1 = LED - 5mm [color="Red (633nm)" package="5 mm [THT]"]
  R1 = Resistor [tolerance=±5% resistance=220 package=THT]
  부품1 = Arduino Uno (Rev3)
  부품2 = Real Time Clock Module - DS1307 RTC Breakout Board
  부품3 = SparkFun ESP8266 Thing  # not connected
  J1 = Piezo Speaker

nets:
  N1: LED1.cathode, R1.Pin_1
  N2: LED1.anode, 부품1.D13/SCK
  GND: R1.Pin_0, 부품1.GND, 부품2.GND, J1.pin1
  N3: 부품1.A4/SDA, 부품2.SDA
  N4: 부품1.A5/SCL, 부품2.SCL
  N5: 부품1.D12/MISO, J1.pin2
  5V: 부품1.5V, 부품2.5V
