# Fritzing sketch id1981_Honduino_0 (saved by Fritzing 0.9.3b)

parts:
  Part1 = Arduino Uno (Rev3)
  Part2 = Bluetooth HC-05 Macho
  LCM1602_IIC1 = generic_ic_dip_22_300mil.fzp [part_number="LCM1602 IIC" chip_label="LCM1602 IIC"]
  LCD1 = LCD screen

nets:
  N1: Part1.A4/SDA, LCM1602_IIC1.connector18
  N2: Part1.A5/SCL, LCM1602_IIC1.connector19
  N3: Part1.D9_PWM, Part2.Key
  N4: Part1.D10_PWM/SS, Part2.TXD
  N5: Part1.D11_PWM/MOSI, Part2.RXD
  3V3: Part1.3V3, Part2.VCC
  N6: Part1.5V, LCM1602_IIC1.connector17
  GND: Part1.GND, Part2.GND, LCM1602_IIC1.connector16
  N7: LCM1602_IIC1.connector0, LCD1.VSS
  N8: LCM1602_IIC1.connector1, LCD1.VDD
  N9: LCM1602_IIC1.connector2, LCD1.V0
  N10: LCM1602_IIC1.connector3, LCD1.RS
  N11: LCM1602_IIC1.connector4, LCD1.R/W
  N12: LCM1602_IIC1.connector5, LCD1.E
  N13: LCM1602_IIC1.connector6, LCD1.DB0
  N14: LCM1602_IIC1.connector7, LCD1.DB1
  N15: LCM1602_IIC1.connector8, LCD1.DB2
  N16: LCM1602_IIC1.connector9, LCD1.DB3
  N17: LCM1602_IIC1.connector10, LCD1.DB4
  N18: LCM1602_IIC1.connector11, LCD1.DB5
  N19: LCM1602_IIC1.connector12, LCD1.DB6
  N20: LCM1602_IIC1.connector13, LCD1.DB7
  N21: LCM1602_IIC1.connector14, LCD1.LED+
  N22: LCM1602_IIC1.connector15, LCD1.LED-
  N23: LCM1602_IIC1.connector20, LCM1602_IIC1.connector21
