# Fritzing sketch id1986_skv_arduino_pro_mini_1_0 (saved by Fritzing 0.7.12b)

parts:
  Part1 = Arduino Pro Mini 3.3V
  LCD = LCD screen
  DS2 = DS18B20_1_Wire_Temperature_Sensor [part_number=DS18B20]
  Rele = Relay [part_number=FRS1B-S package=THT]
  2k2 = resistor.fzp
  DS1 = DS18B20_1_Wire_Temperature_Sensor [part_number=DS18B20]
  Rele1 = Relay [part_number=FRS1B-S package=THT]
  4k7 = resistor.fzp
  DS3 = DS18B20_1_Wire_Temperature_Sensor [part_number=DS18B20]
  R5 = Rotary Potentiometer (Small) [maximum_resistance=10kΩ]
  4k7_2 = resistor.fzp
  4k7_3 = resistor.fzp

nets:
  5V: Part1.VCC, LCD.VDD, LCD.LED+, DS2.connector1, DS1.connector1, 4k7.connector1, DS3.connector1, R5.leg2, 4k7_2.connector1, 4k7_3.connector1
  GND: Part1.GND, LCD.VSS, LCD.R/W, LCD.LED-, DS2.connector3, 2k2.connector1, DS1.connector3, DS3.connector3, R5.leg1
  N1: Part1.A2, R5.wiper
  N2: Part1.A1, Rele1.COIL2
  N3: Part1.A0, Rele.COIL2
  N4: Part1.D10, DS3.connector2, 4k7_3.connector0
  N5: Part1.D9, DS1.connector2, 4k7_2.connector0
  N6: Part1.D8, DS2.connector2, 4k7.connector0
  N7: Part1.D7, LCD.DB7
  N8: Part1.D6, LCD.DB6
  N9: Part1.D5, LCD.DB5
  N10: Part1.D4, LCD.DB4
  N11: Part1.D3, LCD.E
  N12: Part1.D2, LCD.RS
  N13: LCD.V0, 2k2.connector0

notes:
  solar collector controller with arduino pro mini processor, LCD screen and 3 temperature sensors DS18B20
  Pump controll
  relay
  solar collector controller with arduino pro mini processor, LCD screen and 2 temperature sensors DS18B20
  Thermostat relay
