# Fritzing sketch id1987_Hot_wire_arduino_0 (saved by Fritzing 0.9.3b)
circuit board: 8.46667cm x 5.64444cm

parts:
  U1 = 7812
  Q1 = Basic FET N-Channel [part_number=IRF530 package="D2Pak [SMD]"]
  R1 = Resistor [tolerance=±5% resistance=1.5 power=100W package=THT]
  LED1 = LED - 5mm [color="Red (633nm)" package="5 mm [THT]"]
  U2 = POT [package=pot_mammoth]
  Q2 = TRANSISTOR_NPN [part_number=BC547 package=to-92-ammo]
  Q3 = TRANSISTOR_NPN [part_number=BC547 package=to-92-ammo]
  R2 = Resistor [tolerance=±5% resistance=1k package=THT]
  R3 = Resistor [tolerance=±5% resistance=1k package=THT]
  R4 = Resistor [tolerance=±5% resistance=1k package=THT]
  R5 = Resistor [tolerance=±5% resistance=1k package=THT]
  R6 = Resistor [tolerance=±5% resistance=100 package=THT]
  BAT1 = Battery Holders [part_number=9v-20v package=lipo-1100mAh]
  Digispark1 = generic_sip_9_300mil.fzp
  R7 = Resistor [tolerance=±5% resistance=100 package=THT]
  R8 = Resistor [tolerance=±5% resistance=1k package=THT]

nets:
  N1: U1.connector0, R1.Pin_1, BAT1.+
  N2: U1.connector1, Q1.source, U2.E, Q2.E, Q3.E, BAT1.-, Digispark1.connector1
  N3: U1.connector2, R4.Pin_1, Digispark1.connector2
  N4: Q1.Gate, R6.Pin_1
  N5: Q1.drain, R1.Pin_0
  N6: LED1.cathode, R7.Pin_1
  N7: LED1.anode, U2.A, Digispark1.connector0
  N8: U2.S, R8.Pin_1
  N9: Q2.B, R2.Pin_1
  N10: Q2.C, R4.Pin_0, R6.Pin_0
  N11: Q3.B, R3.Pin_1
  N12: Q3.C, R2.Pin_0, R5.Pin_0
  N13: R3.Pin_0, Digispark1.connector4
  N14: Digispark1.connector3, R7.Pin_0
  N15: Digispark1.connector5, R8.Pin_0
