# Fritzing sketch id1988_HotWire_0 (saved by Fritzing 0.9.0b)
breadboards: 1

parts:
  Raspberry_Pi1 = Raspberry_Pi_B+
  LED1 = LED - 5mm [color="Red (633nm)" package="5 mm [THT]"]
  U1 = Buzzer [chip_label=Buzzer]
  R1 = Resistor [tolerance=±5% resistance=1k package=THT]
  R2 = Resistor [tolerance=±5% resistance=220 package=THT]

nets:
  N1: Raspberry_Pi1.connector37, R1.Pin_0, R2.Pin_0
  N2: LED1.cathode, R1.Pin_1
  N3: LED1.anode, U1.connector0
  N4: U1.connector1, R2.Pin_1

notes:
  Simple "hot" wire kids game (similar in notion to Operation)
  1x Red LED
  1x Buzzer
  1x 1K Ohms resistor - LED resistor
  1x 220 Ohms resistor - Buzzer resistor
  1x Single core electrical wire (make a circle in one end and remove cover, pass the circle inside the ochre wire) - this is the yellow one
  1x Single core electrical wire (remove all the cover and create waves and shapes) - this is the ochre one
  The objective of the game is to pass the circle from one end of the ochre wire to the other end, without tripping the buzzer and LED, which go on when the yellow wire touches the ochre.
