# Fritzing sketch id1989_Cutter_0 (saved by Fritzing 0.7.12b)
breadboards: 1

parts:
  Arduino1 = Arduino
  LCD1 = LCD screen
  Status_LED = LED - 3mm [color="Red (633nm)" package="3 mm [THT]"]
  Status_LED_Current_Limit = Resistor [tolerance=±5% resistance=100 package=THT]
  Duty_Control = Rotary Potentiometer (Small) [maximum_resistance=10kΩ]
  button_pull-up = Resistor [tolerance=±5% resistance=10k package=THT]
  10k_Contrast = Resistor [tolerance=±5% resistance=10k package=THT]
  1k_Contrast = Resistor [tolerance=±5% resistance=1k package=THT]
  Rsense = Resistor [tolerance=±5% resistance=300 package=THT]
  Isense_FET = basic_fet_n.fzp
  +5v_Regulator = Voltage Regulator - 5V [package="TO220 [THT]"]
  Enable/Disable = Pushbutton [package="[THT]"]
  Connection_for_Cutter = Screw terminal - 2 pins [package=THT]
  20V_7_5A = Screw terminal - 2 pins [package=THT]
  IC2 = DIP___8_pins [part_number=LM741]
  IC3 = DIP___8_pins [part_number=LM741]

nets:
  GND: Arduino1.GND, LCD1.VSS, LCD1.R/W, LCD1.DB0, LCD1.DB1, LCD1.DB2, LCD1.DB3, LCD1.LED-, Status_LED_Current_Limit.Pin_0, Duty_Control.leg2, 1k_Contrast.Pin_1, Isense_FET.connector4, +5v_Regulator.GND, Enable/Disable.Pin_3, Enable/Disable.Pin_4, 20V_7_5A.pin1
  N1: Arduino1.D13, Status_LED.anode
  RS: Arduino1.D12, LCD1.RS
  E: Arduino1.D11, LCD1.E
  DB4: Arduino1.D10, LCD1.DB4
  DB5: Arduino1.D9, LCD1.DB5
  DB6: Arduino1.D8, LCD1.DB6
  DB7: Arduino1.D7, LCD1.DB7
  N2: Arduino1.D3, Isense_FET.connector0
  N3: Arduino1.D2, button_pull-up.Pin_1, Enable/Disable.Pin_1, Enable/Disable.Pin_2
  5V: Arduino1.+5V, LCD1.VDD, LCD1.LED+, Duty_Control.leg1, button_pull-up.Pin_0, 10k_Contrast.Pin_1, +5v_Regulator.output_voltage, IC2.connector6, IC3.connector6
  N4: Arduino1.A0, Duty_Control.wiper
  Current Feedback -> ADC: Arduino1.A5, IC3.connector5
  N5: LCD1.V0, 10k_Contrast.Pin_0, 1k_Contrast.Pin_0
  N6: Status_LED.cathode, Status_LED_Current_Limit.Pin_1
  N7: Rsense.Pin_0, IC2.connector5, IC3.connector1
  N8: Rsense.Pin_1, Isense_FET.connector1, IC2.connector1
  N9: Isense_FET.connector2, Connection_for_Cutter.pin1
  N10: Isense_FET.connector3, IC2.connector2, IC3.connector2
  20V: +5v_Regulator.input_voltage, Connection_for_Cutter.pin2, 20V_7_5A.pin2
  -5V: IC2.connector3, IC3.connector3

notes:
  Hotwire Foam Cutter, 1
