# Fritzing sketch id198_test01_0 (saved by Fritzing 0.9.3b)

parts:
  부품1 = Arduino Uno (Rev3)
  부품2 = Real Time Clock Module - DS1307 RTC Breakout Board
  부품3 = SparkFun ESP8266 Thing  # not connected
  J1 = Piezo Speaker

nets:
  N1: 부품1.A4/SDA, 부품2.SDA
  N2: 부품1.A5/SCL, 부품2.SCL
  N3: 부품1.D11_PWM/MOSI, J1.pin2
  GND: 부품1.GND, 부품2.GND, J1.pin1
  5V: 부품1.5V, 부품2.5V
