# Fritzing sketch id1994_gameclock (saved by Fritzing 0.9.3b)
breadboards: 1

parts:
  Componente1 = Arduino Uno (Rev3)
  LCD1 = LCD screen
  J1 = Piezo Speaker
  R1 = Rotary Potentiometer (Small) [maximum_resistance=100kΩ package=THT]
  S1 = Pushbutton [package="[THT]"]
  S3 = Pushbutton [package="[THT]"]
  R3 = Resistor [tolerance=±5% resistance=10k package=THT]
  R4 = Resistor [tolerance=±5% resistance=10k package=THT]
  R5 = Resistor [tolerance=±5% resistance=10k package=THT]
  C4 = Ceramic Capacitor [capacitance=100nF package="100 mil [THT, multilayer]"]
  C6 = Ceramic Capacitor [capacitance=100nF package="100 mil [THT, multilayer]"]
  S2 = Pushbutton [package="[THT]"]
  C5 = Ceramic Capacitor [capacitance=100nF package="0603 [SMD, multilayer]"]

nets (from the breadboard view):
  N1: Componente1.D8, S1.Pin_3, S1.Pin_4, R3.Pin_0, C5.0
  N2: Componente1.D9_PWM, R4.Pin_0, C4.0, S2.Pin_3, S2.Pin_4
  N3: Componente1.D10_PWM/SS, S3.Pin_3, S3.Pin_4, R5.Pin_0, C6.0
  N4: Componente1.D12/MISO, J1.pin2
  N5: Componente1.D2, LCD1.DB7
  N6: Componente1.D3_PWM, LCD1.DB6
  N7: Componente1.D4, LCD1.DB5
  N8: Componente1.D5_PWM, LCD1.DB4
  N9: Componente1.D6_PWM, LCD1.E
  N10: Componente1.D7, LCD1.RS
  5V: Componente1.5V, LCD1.VDD, R1.leg2, S1.Pin_1, S1.Pin_2, S3.Pin_1, S3.Pin_2, C4.1, C6.1, S2.Pin_1, S2.Pin_2, C5.1
  GND: Componente1.GND, LCD1.VSS, LCD1.R/W, J1.pin1, R1.leg1, R3.Pin_1, R4.Pin_1, R5.Pin_1
  N11: LCD1.V0, R1.wiper
