# Fritzing sketch id1995_conectar_un_lcd_qy_1602_a_un_arduino_uno_r3_0 (saved by Fritzing 0.7.1b)
breadboards: 1

parts:
  Arduino1 = Arduino
  LCD1 = LCD screen
  R1 = Rotary Potentiometer (Small) [maximum_resistance=5kΩ]

nets:
  GND: Arduino1.GND, LCD1.VSS, LCD1.R/W, LCD1.LED-, R1.leg1
  N1: Arduino1.D12, LCD1.RS
  N2: Arduino1.D11, LCD1.E
  N3: Arduino1.D5, LCD1.DB4
  N4: Arduino1.D4, LCD1.DB5
  N5: Arduino1.D3, LCD1.DB6
  N6: Arduino1.D2, LCD1.DB7
  +5V: Arduino1.+5V, LCD1.VDD, LCD1.LED+, R1.leg2
  N7: LCD1.V0, R1.wiper

notes:
  Arduino code
  // include the library code:
  #include <LiquidCrystal.h>
  // initialize the library with the numbers of the interface pins
  LiquidCrystal lcd(12, 11, 5, 4, 3, 2);
  void setup() {
  // set up the LCD's number of columns and rows:
  lcd.begin(16, 2);
  }
  void loop() {
  lcd.setCursor(0,0);
  // Print a message to the LCD.
  lcd.print("EstoNoEsUnPoema");
  // set the cursor to column 0, line 2
  // (note: line 2 is the second row, since first row is 0):
  lcd.setCursor(0, 2);
  // print the number of seconds since reset:
  lcd.print(millis()/1000);
  }
