# Fritzing sketch id1996_Woosh_ESP12ConnectUp_0 (saved by Fritzing 0.9.3b)
circuit board: 8.46667cm x 5.64444cm
breadboards: 1

parts:
  ESP12E = ESP12E
  R1 = Resistor [tolerance=±5% resistance=10k package=THT]
  S1 = Pushbutton [package=THT]
  D2 = Schottky Diode [part_number=1N5817 package="300 mil [THT]"]
  D1 = Schottky Diode [part_number=1N5817 package="300 mil [THT]"]
  R2 = Resistor [tolerance=±5% resistance=10k package=THT]
  R3 = Resistor [tolerance=±5% resistance=10k package=THT]
  R4 = Resistor [tolerance=±5% resistance=10k package=THT]
  R5 = Resistor [tolerance=±5% resistance=10k package=THT]
  R6 = Resistor [tolerance=±5% resistance=10k package=THT]
  R7 = Resistor [tolerance=±5% resistance=100k package=THT]
  R8 = Resistor [tolerance=±5% resistance=220k package=THT]
  C3 = Tantalum Capacitor [capacitance=47µF part_number=100u package="200 mil [THT, tantalum]"]
  C1 = Capacitor [part_number=100n package=cap-pth-large]
  C2 = Capacitor [part_number=100n package=cap-pth-large]

nets:
  CP2102 RCV: ESP12E.connector0
  N1: ESP12E.connector1, R1.Pin_1, D2.anode
  N2: ESP12E.connector4, S1.leg0, R3.Pin_0
  N3: ESP12E.connector5, R2.Pin_0
  N4: ESP12E.connector6, R4.Pin_0
  GND: ESP12E.connector7, S1.leg1, R4.Pin_1, R7.Pin_1
  N5: ESP12E.connector16, ESP12E.connector17
  3.3v: ESP12E.connector22, R1.Pin_0, D1.cathode, R2.Pin_1, R3.Pin_1, R5.Pin_1, R6.Pin_0, C3.+, C2.2
  N6: ESP12E.connector26, ESP12E.connector29, R5.Pin_0
  N7: ESP12E.connector27, D1.anode, R6.Pin_1, C1.2
  N8: ESP12E.connector28, R7.Pin_0, R8.Pin_1
  CP2102 Xmit: D2.cathode
  A0 in: R8.Pin_0
  N9: C3.-, C2.1
  CP2102/DTR: C1.1

notes:
  Close Switch to   Upload Pgm
