# Fritzing sketch id1997_Project1_0 (saved by Fritzing 0.8.7b)
breadboards: 1

parts:
  J1 = Piezo Speaker
  Part1 = Arduino Uno (Rev3)
  LED1 = LED - 5mm [color="Red (633nm)" package="5 mm [THT]"]
  LED2 = LED - 5mm [color="Red (633nm)" package="5 mm [THT]"]
  LED3 = LED - 5mm [color="Red (633nm)" package="5 mm [THT]"]
  LED4 = LED - 5mm [color="Red (633nm)" package="5 mm [THT]"]
  LED5 = LED - 5mm [color="Red (633nm)" package="5 mm [THT]"]
  LED7 = LED - 5mm [color="Blue (525nm)" package="5 mm [THT]"]
  R1 = Resistor [tolerance=±5% resistance=220 package=THT]
  R2 = Resistor [tolerance=±5% resistance=220 package=THT]
  R3 = Resistor [tolerance=±5% resistance=220 package=THT]
  R4 = Resistor [tolerance=±5% resistance=220 package=THT]
  R5 = Resistor [tolerance=±5% resistance=220 package=THT]
  R6 = Resistor [tolerance=±5% resistance=220 package=THT]
  R7 = Resistor [tolerance=±5% resistance=220 package=THT]
  R8 = Resistor [tolerance=±5% resistance=220 package=THT]
  R9 = Resistor [tolerance=±5% resistance=220 package=THT]
  R10 = Resistor [tolerance=±5% resistance=220 package=THT]
  R11 = Resistor [tolerance=±5% resistance=330 package=THT]
  S1 = Pushbutton [package="[THT]"]
  R13 = Resistor [tolerance=±5% resistance=10k package=THT]
  VCC1 = Battery block 9V
  LED11 = LED - 5mm [color="Blue (525nm)" package="5 mm [THT]"]
  LED12 = LED - 5mm [color="Blue (525nm)" package="5 mm [THT]"]
  LED13 = LED - 5mm [color="Blue (525nm)" package="5 mm [THT]"]
  LED14 = LED - 5mm [color="Blue (525nm)" package="5 mm [THT]"]

nets:
  N1: J1.pin1, Part1.GND, R1.Pin_1, R2.Pin_1, R3.Pin_1, R4.Pin_1, R5.Pin_1, R6.Pin_1, R8.Pin_1, R10.Pin_1, R11.Pin_1, R13.Pin_1, VCC1.-
  N2: J1.pin2, Part1.D13/SCK
  N3: Part1.D8, LED7.anode
  N4: Part1.D9_PWM, LED11.anode
  N5: Part1.D10_PWM/SS, LED12.anode
  N6: Part1.D11_PWM/MOSI, LED14.anode
  N7: Part1.D12/MISO, R7.Pin_0, LED13.cathode
  N8: Part1.D2, S1.Pin_1, S1.Pin_2, R13.Pin_0
  N9: Part1.D3_PWM, LED1.anode
  N10: Part1.D4, LED2.anode
  N11: Part1.D5_PWM, LED3.anode
  N12: Part1.D6_PWM, LED4.anode
  N13: Part1.D7, LED5.anode
  N14: Part1.5V, S1.Pin_3, S1.Pin_4
  N15: Part1.VIN, VCC1.+
  N16: LED1.cathode, R1.Pin_0
  N17: LED2.cathode, R4.Pin_0
  N18: LED3.cathode, R5.Pin_0
  N19: LED4.cathode, R3.Pin_0
  N20: LED5.cathode, R6.Pin_0
  N21: LED7.cathode, R8.Pin_0
  N22: R2.Pin_0, LED12.cathode
  N23: R9.Pin_0, LED11.cathode
  N24: R10.Pin_0, LED14.cathode
