# Fritzing sketch id1998_Untitled_Sketch_2_0 (saved by Fritzing 0.9.2b)
breadboards: 1

parts:
  Ultrasonic = generic_sip_4_300mil.fzp [chip_label=IC]
  Arduino = Arduino Uno (Rev3)
  J1 = Piezo Speaker

nets:
  N1: Ultrasonic.connector0, Arduino.5V
  N2: Ultrasonic.connector1, Arduino.D11_PWM/MOSI
  N3: Ultrasonic.connector2, Arduino.D12/MISO
  N4: Ultrasonic.connector3, Arduino.GND, J1.pin1
  N5: Arduino.D10_PWM/SS, J1.pin2
