# Fritzing sketch id1999_LDR_0 (saved by Fritzing 0.9.2b)
breadboards: 1

parts:
  Part1 = Arduino Mega 2560 (Rev3)
  R1 = Photocell (LDR) [package=THT]
  R2 = Resistor [tolerance=±5% resistance=180k package=THT]
  LED1 = smd LED [color="White (6500K)" package="0603 [SMD]"]
  R3 = Resistor [tolerance=±5% resistance=1k package=THT]

nets:
  N1: Part1.A0, R1.pin_0, R2.Pin_0
  N2: Part1.D12_PWM, LED1.anode
  N3: Part1.5V, R2.Pin_1, R3.Pin_1
  N4: Part1.GND, R1.pin_1
  N5: LED1.cathode, R3.Pin_0
