# Fritzing sketch id19_Untitled_Sketch_0 (saved by Fritzing 0.9.3b)
breadboards: 1

parts:
  Part1 = Arduino Uno (Rev3)
  IR1 = TSOP312.., 314.. [package=THT]
  R1 = Resistor [tolerance=±5% resistance=330 package=THT]
  R2 = Resistor [tolerance=±5% resistance=100 package=THT]
  R3 = Resistor [tolerance=±5% resistance=100 package=THT]
  R4 = Resistor [tolerance=±5% resistance=100 package=THT]
  LED1 = LED - 5mm [color="Red (633nm)" package="5 mm [THT]"]
  LED2 = LED - 5mm [color="Yellow (595nm)" package="5 mm [THT]"]
  LED3 = LED - 5mm [color="Blue (430nm)" package="5 mm [THT]"]
  DI1 = 7-Segment LED Display [package=THT]

nets:
  N1: Part1.D8, DI1.cathodeC
  N2: Part1.D9_PWM, DI1.cathodeDP
  N3: Part1.D10_PWM/SS, DI1.cathodeG
  N4: Part1.D11_PWM/MOSI, DI1.cathodeF
  N5: Part1.D12/MISO, DI1.cathodeA
  N6: Part1.D13/SCK, DI1.cathodeB
  N7: Part1.D2, IR1.GND
  N8: Part1.D3_PWM, R3.Pin_1
  N9: Part1.D4, R4.Pin_1
  N10: Part1.D5_PWM, R2.Pin_1
  N11: Part1.D6_PWM, DI1.cathodeE
  N12: Part1.D7, DI1.cathodeD
  N13: Part1.5V, R1.Pin_1, LED1.cathode, LED2.cathode, LED3.cathode
  N14: Part1.GND, IR1.Vs, DI1.commAnode#7
  N15: IR1.Data, R1.Pin_0
  N16: R2.Pin_0, LED1.anode
  N17: R3.Pin_0, LED3.anode
  N18: R4.Pin_0, LED2.anode
