# Fritzing sketch id1_svetofor_0 (saved by Fritzing 0.9.3b)
circuit board: 8.46667cm x 5.64444cm
breadboards: 1

parts:
  Часть1 = Arduino Uno (Rev3)
  R1 = Resistor [tolerance=±5% resistance=220 package=THT]
  R2 = Resistor [tolerance=±5% resistance=220 package=THT]
  R3 = Resistor [tolerance=±5% resistance=220 package=THT]
  LED1 = LED - 5mm [color="Red (633nm)" package="5 mm [THT]"]
  LED2 = LED - 5mm [color="Yellow (595nm)" package="5 mm [THT]"]
  LED3 = LED - 5mm [color="Green (560nm)" package="5 mm [THT]"]

nets:
  N1: Часть1.D8, R3.Pin_0
  N2: Часть1.D10_PWM/SS, R2.Pin_0
  N3: Часть1.D12/MISO, R1.Pin_0
  N4: Часть1.GND, LED1.cathode, LED2.cathode, LED3.cathode
  N5: R1.Pin_1, LED3.anode
  N6: R2.Pin_1, LED2.anode
  N7: R3.Pin_1, LED1.anode
