# Fritzing sketch id2000_Ethernet_relay_switch_0 (saved by Fritzing 0.9.3b)

parts:
  Part1 = richardbruneau000
  Part2 = Arduino Uno (Rev3) - ICSP
  U1 = 2ChannelRelay

nets:
  N1: Part1.connector8, Part2.3V3
  N2: Part1.connector9, Part2.GND
  N3: Part1.connector11, Part2.D10_PWM/SS
  N4: Part1.connector12, Part2.D11_PWM/MOSI
  N5: Part1.connector13, Part2.D13/SCK
  N6: Part1.connector15, Part2.D12/MISO
  N7: Part2.A0, U1.connector2
  N8: Part2.A1, U1.connector3
  N9: Part2.5V, U1.connector0
