# Fritzing sketch id2002_ESP8266_PCF8574_0 (saved by Fritzing 0.9.3b)

parts:
  U1 = NodeMCU
  U2 = PCF8574 [package="DIP16 [THT]"]
  IC1 = ULN2803A [package=THT]
  R4 = Resistor [tolerance=±5% resistance=10k package=THT]
  R5 = Resistor [tolerance=±5% resistance=10k package=THT]
  R6 = Resistor [tolerance=±5% resistance=10k package=THT]
  R7 = Resistor [tolerance=±5% resistance=10k package=THT]
  R8 = Resistor [tolerance=±5% resistance=10k package=THT]
  R9 = Resistor [tolerance=±5% resistance=10k package=THT]
  R10 = Resistor [tolerance=±5% resistance=10k package=THT]
  R11 = Resistor [tolerance=±5% resistance=10k package=THT]
  U3 = RELAY [package=relay-t9a]
  U4 = RELAY [package=relay-t9a]
  U5 = RELAY [package=relay-t9a]
  U6 = RELAY [package=relay-t9a]
  S3 = Square Pushbutton
  S4 = Square Pushbutton
  S5 = Square Pushbutton
  S6 = Square Pushbutton
  V1 = DC Power [voltage=5]

nets:
  N1: U1.connector1, U2.SDA
  N2: U1.connector2, U2.SCL
  N3: U1.connector7, U2.INT
  N4: U1.connector13, U2.A0, U2.A1, U2.A3, U2.GND, IC1.0V, U3.COIL1, U4.COIL1, U5.COIL1, U6.COIL1, S3.leg1, S4.leg1, S5.leg1, S6.leg1, V1.V-
  N5: U1.connector14, U2.VCC
  N6: U1.connector15, IC1.COM_-_Common, V1.V+
  N7: U2.P0, IC1.In_4, R9.Pin_0
  N8: U2.P1, IC1.In_3, R10.Pin_0
  N9: U2.P2, IC1.In_2, R8.Pin_0
  N10: U2.P3, IC1.In_1, R11.Pin_0
  N11: U2.P4, R7.Pin_0
  N12: U2.P5, R6.Pin_0
  N13: U2.P6, R5.Pin_0
  N14: U2.P7, R4.Pin_0
  N15: IC1.Out_4, U6.COIL2
  N16: IC1.Out_3, U5.COIL2
  N17: IC1.Out_2, U4.COIL2
  N18: IC1.Out_1, U3.COIL2
  N19: R4.Pin_1, R5.Pin_1, R6.Pin_1, R7.Pin_1, R8.Pin_1, R9.Pin_1, R10.Pin_1, R11.Pin_1, S3.leg0, S4.leg0, S5.leg0, S6.leg0
