# Fritzing sketch id2003_Fritzing_0 (saved by Fritzing 0.8.5b)
circuit board: 4.3cm x 4.5cm
breadboards: 1

parts:
  IC1 = Voltage Regulator [package=to-220-alt]  # not connected
  R1 = Resistor [tolerance=±5% resistance=220 package=THT]
  FSR1 = Basic Force Sensing Resistor (FSR) [package=THT]
  R2 = Resistor [tolerance=±5% resistance=220 package=THT]
  R3 = Resistor [tolerance=±5% resistance=220 package=THT]
  R4 = Resistor [tolerance=±5% resistance=220 package=THT]
  FSR4 = Basic Force Sensing Resistor (FSR) [package=THT]
  FSR2 = Basic Force Sensing Resistor (FSR) [package=THT]
  FSR3 = Basic Force Sensing Resistor (FSR) [package=THT]
  ACLRMTR = female pin header, 4 pins [form="♀ (female)"]
  Teensy = Teensy 2.0

nets:
  N1: R1.Pin_0, FSR1.pin_0, Teensy.F0
  N2: R1.Pin_1, R2.Pin_1, R3.Pin_1, R4.Pin_1, ACLRMTR.pin3, Teensy.GND
  N3: FSR1.pin_1, FSR4.pin_1, FSR2.pin_1, FSR3.pin_1, ACLRMTR.pin4, Teensy.VCC
  N4: R2.Pin_0, FSR2.pin_0, Teensy.F1
  N5: R3.Pin_0, FSR3.pin_0, Teensy.F4
  N6: R4.Pin_0, FSR4.pin_0, Teensy.F5
  N7: ACLRMTR.pin1, Teensy.D1
  N8: ACLRMTR.pin2, Teensy.D0

notes:
  Wii Nunchuck
  SDA (violett) - SCL(gelb) - GND - VCC
  HPSTR Pyramid
  vcc
  GND
  SCL
  SDA
