# Fritzing sketch id2004_Untitled_Sketch_0 (saved by Fritzing 0.9.3b)
circuit board: 8.46667cm x 5.64444cm
breadboards: 2

parts:
  Composant1 = Arduino Mega ADK (Rev3)
  LED4 = smd LED [color="Red (633nm)" package="0603 [SMD]"]
  LED5 = RGB LED (com. cathode, rgb) [package="5 mm [THT]"]
  LED6 = RGB LED (com. cathode, rgb) [package="5 mm [THT]"]
  LED7 = RGB LED (com. cathode, rgb) [package="5 mm [THT]"]
  S1 = Momentary Switch [package=ksa_sealed_tac_switch]
  S2 = Momentary Switch [package=ksa_sealed_tac_switch]
  S3 = Momentary Switch [package=ksa_sealed_tac_switch]
  R1 = Resistor [tolerance=±5% resistance=220 package=THT]
  R2 = Resistor [tolerance=±5% resistance=220 package=THT]
  R3 = Resistor [tolerance=±5% resistance=220 package=THT]
  S4 = Pushbutton [package="[THT]"]
  7_Segment1 = 7 Segment Display
  R7 = Resistor [tolerance=±5% resistance=220 package=THT]  # not connected
  R8 = Resistor [tolerance=±5% resistance=220 package=THT]  # not connected

nets (from the schematic view):
  N1: Composant1.GND, Composant1.D30, LED4.cathode, LED5.common_cathode, LED6.common_cathode, LED7.common_cathode, R1.Pin_1, R3.Pin_1, 7_Segment1.Segment_G, 7_Segment1.Segment_F, 7_Segment1.common_anode, 7_Segment1.Segment_E, 7_Segment1.Segment_D, 7_Segment1.Segment_DP, 7_Segment1.Segment_C, 7_Segment1.Segment_B, 7_Segment1.Segment_A
  N2: Composant1.D22, LED4.anode
  N3: Composant1.D24, Composant1.D25
  N4: Composant1.D26, Composant1.D27
  N5: Composant1.D28, Composant1.D29
  N6: LED5.red_anode, LED6.blue_anode, LED7.green_anode, S3.2, S3.4
  N7: LED5.green_anode, LED6.red_anode, LED7.blue_anode, S2.2, S2.4
  N8: LED5.blue_anode, LED6.green_anode, LED7.red_anode, S1.2, S1.4
  N9: S1.1, S1.3, R1.Pin_0
  N10: S2.1, S2.3, R2.Pin_0
  N11: S3.1, R3.Pin_0
  N12: S4.Pin_1, S4.Pin_2, S4.Pin_3, S4.Pin_4

notes:
  sur mais compliqué
