# Fritzing sketch id2005_sketch_0 (saved by Fritzing 0.9.1b)
breadboards: 1

parts:
  Part1 = Arduino Uno (Rev3)
  LED1 = LED - 5mm [color="Red (633nm)" package="5 mm [THT]"]
  LED2 = LED - 5mm [color="Red (633nm)" package="5 mm [THT]"]
  LED3 = LED - 5mm [color="Red (633nm)" package="5 mm [THT]"]
  LED4 = LED - 5mm [color="Red (633nm)" package="5 mm [THT]"]
  LED5 = LED - 5mm [color="Red (633nm)" package="5 mm [THT]"]
  LED6 = LED - 5mm [color="Red (633nm)" package="5 mm [THT]"]
  LED7 = LED - 5mm [color="Red (633nm)" package="5 mm [THT]"]
  LED8 = LED - 5mm [color="Red (633nm)" package="5 mm [THT]"]
  LED9 = LED - 5mm [color="Red (633nm)" package="5 mm [THT]"]
  R1 = Resistor [package="2512 [SMD]"]
  R2 = Resistor [package="2512 [SMD]"]
  R3 = Resistor [package="2512 [SMD]"]
  R4 = Resistor [package="2512 [SMD]"]
  R5 = Resistor [package="2512 [SMD]"]
  R6 = Resistor [package="2512 [SMD]"]
  R7 = Resistor [package="2512 [SMD]"]
  R8 = Resistor [package="2512 [SMD]"]
  R9 = Resistor [package="2512 [SMD]"]
  R10 = Trimmer Potentiometer [maximum_resistance=10kΩ package=THT]
  J1 = Infrared Proximity Sensor
  SPKR1 = Loudspeaker

nets:
  N1: Part1.A0, R10.wiper
  N2: Part1.A3, J1.Vout
  N3: Part1.D8, LED8.anode
  N4: Part1.D9_PWM, LED9.anode
  N5: Part1.D13/SCK, J1.Vcc
  GND: Part1.GND, R1.Pin_1, R2.Pin_1, R3.Pin_1, R4.Pin_1, R5.Pin_1, R6.Pin_1, R7.Pin_1, R8.Pin_1, R9.Pin_1, R10.leg1, J1.GND, SPKR1.pin1
  N6: Part1.D2, LED6.anode
  N7: Part1.D3_PWM, LED1.anode
  N8: Part1.D4, LED3.anode
  N9: Part1.D5_PWM, LED4.anode
  N10: Part1.D6_PWM, LED5.anode
  N11: Part1.D7, LED7.anode
  N12: Part1.5V, R10.leg2
  N13: LED1.cathode, R2.Pin_0
  N14: LED2.cathode, R3.Pin_0
  N15: LED3.cathode, R4.Pin_0
  N16: LED4.cathode, R5.Pin_0
  N17: LED5.cathode, R6.Pin_0
  N18: LED6.cathode, R1.Pin_0
  N19: LED7.cathode, R7.Pin_0
  N20: LED8.cathode, R8.Pin_0
  N21: LED9.cathode, R9.Pin_0

notes:
  Ultrasonics sensor HC-SR4
  Could be any analog speaker like:
  - a piezo-electric one
  - a real boombox
  - an earbud
  These are not mission-critical, but do provide input useful for debuging when no sound comes out (they visualise the pitch)
  Hold both of these in your hand. Clench your fist to conduct more electricity. It's best to use a crocodile here.
  This turns the device on and of (practical to cut out the sound ICE)
