# Fritzing sketch id2008_photocell_LED_0 (saved by Fritzing 0.7.4b)
breadboards: 1

parts:
  Arduino1 = Arduino
  R1 = Photocell (LDR) [package=THT]
  R2 = Resistor [tolerance=±20% resistance=100k package=THT]
  LED2 = LED - 5mm [color="Red (633nm)" package="5 mm [THT]"]

nets:
  N1: Arduino1.GND, R1.pin_1, LED2.cathode
  N2: Arduino1.D13, LED2.anode
  N3: Arduino1.+5V, R2.Pin_0
  N4: Arduino1.A0, R1.pin_0, R2.Pin_1
