# Fritzing sketch id2009_Humidity_and_temp_on__20x4_LCD_0 (saved by Fritzing 0.9.3b)
breadboards: 1

parts:
  Part1 = Arduino Uno (Rev3)
  LCD_20x4_I2C = Grove OLED 128x96
  RHT1 = Humidity and Temperature Sensor RHT03

nets:
  N1: Part1.A4/SDA, LCD_20x4_I2C.SDA
  N2: Part1.A5/SCL, LCD_20x4_I2C.SCL
  N3: Part1.D2, RHT1.Data-signal
  VCC: Part1.5V, LCD_20x4_I2C.VCC, RHT1.Vcc
  GND: Part1.GND, LCD_20x4_I2C.GND, RHT1.GND_2
