# Fritzing sketch id200_PhotoCellCircuit_0 (saved by Fritzing 0.9.2b)
breadboards: 1

parts:
  Part1 = Arduino Uno (Rev3)
  R1 = Resistor [tolerance=±5% resistance=10k package=THT]
  R2 = Photocell (LDR) [package=THT]

nets:
  N1: Part1.A0, R1.Pin_1
  N2: R1.Pin_0, R2.pin_0

notes:
  Breadboard
  Arduino UNO Development Board
  Photo Cell Sensor
  10-K Ohm Resistor
  Power
  Ground
