# Fritzing sketch id2010_Untitled_Sketch_0 (saved by Fritzing 0.9.3b)
circuit board: 8.46667cm x 5.64444cm
breadboards: 1

parts:
  RHT1 = Humidity and Temperature Sensor RHT03
  Part2 = Arduino Uno (Rev3) - ICSP
  R1 = Resistor [tolerance=±5% resistance=1k package=THT]

nets:
  VCC: RHT1.Vcc, Part2.5V, R1.Pin_0
  N1: RHT1.Data-signal, Part2.D2, R1.Pin_1
  N2: RHT1.GND_2, Part2.GND
