# Fritzing sketch id2011_huzzah8266_MPU_6050_0 (saved by Fritzing 0.9.3b)

parts:
  Adafruit_HUZZAH_ESP8266_Breakout1 = Adafruit HUZZAH ESP8266 Breakout [part_number=2471]
  MPU-6050 = MPU-6050 GY-521 [form="♀ (female)"]

nets:
  N1: Adafruit_HUZZAH_ESP8266_Breakout1.#5, MPU-6050.connector2
  N2: Adafruit_HUZZAH_ESP8266_Breakout1.#4, MPU-6050.connector3
  N3: Adafruit_HUZZAH_ESP8266_Breakout1.3V, MPU-6050.connector0
  N4: Adafruit_HUZZAH_ESP8266_Breakout1.GND, MPU-6050.connector1
