# Fritzing sketch id2012_huzzah_dotstar_0 (saved by Fritzing 0.9.3b)
breadboards: 1

parts:
  Part1 = adafruit [part_number="Adafruit #2821"]
  JACK1 = 2.1mm_Barrel_Jack_with_Terminal_Block
  NEOPIXEL1 = Neopixel_Strip_White_30_m
  U2 = PSG [part_number=SN74AHCT125]

nets:
  N1: Part1.connector60, U2.connector10
  N2: Part1.connector61, U2.connector7
  N3: JACK1.connector1, NEOPIXEL1.connector3, U2.connector13
  N4: JACK1.connector2, NEOPIXEL1.connector1, U2.connector6, U2.connector9, U2.connector12
  N5: NEOPIXEL1.connector2, U2.connector8, U2.connector11
