# Fritzing sketch id2013_HVAC_0 (saved by Fritzing 0.9.1b)
circuit board: 4.48228cm x 5.30326cm
breadboards: 1

parts:
  Onderdeel1 = Arduino Micro (Rev3)
  LCD1 = LCD screen
  S1 = Pushbutton [package="[THT]"]
  S2 = Pushbutton [package="[THT]"]
  S3 = Pushbutton [package="[THT]"]
  Q1 = Basic FET N-Channel [package="TO220 [THT]"]
  R1 = Resistor [tolerance=±5% resistance=10k package=THT]
  R2 = Resistor [tolerance=±5% resistance=1M package=THT]
  RHT1 = Humidity and Temperature Sensor RHT03
  J1 = female pin header, 2 pins [form="♀ (female)"]  # not connected

nets (from the breadboard view):
  GND: Onderdeel1.GND, LCD1.VSS, LCD1.V0, LCD1.R/W, LCD1.LED-, S1.Pin_1, S1.Pin_2, S2.Pin_1, S2.Pin_2, S3.Pin_1, S3.Pin_2, R2.Pin_0, RHT1.GND_2
  N1: Onderdeel1.D2/SDA, Q1.gate
  N2: Onderdeel1.D3/SCL, R1.Pin_1, RHT1.Data-signal
  N3: Onderdeel1.D4_PWM/A6, LCD1.DB7
  N4: Onderdeel1.D5_PWM, LCD1.DB6
  N5: Onderdeel1.D6_PWM/A7, LCD1.DB5
  N6: Onderdeel1.D7, LCD1.DB4
  N7: Onderdeel1.D8_PWM/A8, LCD1.E
  N8: Onderdeel1.D9_PWM/A9, LCD1.RS
  5V: Onderdeel1.5V, LCD1.VDD, LCD1.LED+, R1.Pin_0, RHT1.Vcc
  N9: Onderdeel1.A5, S1.Pin_3, S1.Pin_4
  N10: Onderdeel1.A4, S2.Pin_3, S2.Pin_4
  N11: Onderdeel1.A3, S3.Pin_3, S3.Pin_4
  N12: Q1.source, R2.Pin_1
