# Fritzing sketch id2014_HW1_Sketch_0 (saved by Fritzing 0.9.3b)
breadboards: 1

parts:
  元件1 = Photon
  J1 = Basic Servo
  元件2 = Breakout Board for Electret Microphone
  LED1 = LEDs [package=led10mm]
  R1 = Resistor [tolerance=±5% resistance=220 package="0402 [SMD]"]

nets:
  N1: 元件1.A0, 元件2.VCC
  N2: 元件1.A5, J1.pulse
  GND: 元件1.GND, J1.gnd, 元件2.GND, LED1.C
  VIN: 元件1.VIN, J1.vcc, 元件2.AUD
  N3: 元件1.D3, R1.Pin_1
  N4: LED1.A, R1.Pin_0
