# Fritzing sketch id2015_gasSensor_0 (saved by Fritzing 0.6.3b)
breadboards: 1

parts:
  Arduino1 = Arduino
  J1 = female pin header, 2 pins [form="♀ (female)"]
  J2 = female pin header, 2 pins [form="♀ (female)"]
  J3 = female pin header, 2 pins [form="♀ (female)"]
  J4 = female pin header, 2 pins [form="♀ (female)"]
  R1 = Rotary Potentiometer (Small)
  Figaro_TGS_2602_Gas_Sensor1 = Figaro TGS 2602 Gas Sensor

nets:
  N1: Arduino1.GND, J3.pin1, J4.pin1, R1.leg1, Figaro_TGS_2602_Gas_Sensor1.connector2
  N2: Arduino1.+5V, J1.pin2, J2.pin2, J3.pin2, J4.pin2, Figaro_TGS_2602_Gas_Sensor1.connector4, Figaro_TGS_2602_Gas_Sensor1.connector5
  N3: Arduino1.A0, R1.wiper
  N4: J1.pin1, J2.pin1
  N5: R1.leg2, Figaro_TGS_2602_Gas_Sensor1.connector3

notes:
  mctouch
