# Fritzing sketch id2016_lcdhelp_0 (saved by Fritzing 0.9.2b)
breadboards: 1

parts:
  Onderdeel1 = Arduino Uno (Rev3)
  LCD1 = LCD screen

nets:
  GND: Onderdeel1.GND, LCD1.VSS, LCD1.R/W
  N1: Onderdeel1.D2, LCD1.DB2
  N2: Onderdeel1.D3_PWM, LCD1.DB3
  N3: Onderdeel1.D4, LCD1.DB4
  N4: Onderdeel1.D5_PWM, LCD1.DB5
  N5: Onderdeel1.D6_PWM, LCD1.DB6
  N6: Onderdeel1.D7, LCD1.DB7
  5V: Onderdeel1.5V, LCD1.VDD
