# Fritzing sketch id2017_example_car_2_0 (saved by Fritzing 0.9.1b)
breadboards: 1

parts:
  IC1 = H-Bridge [package=THT]
  Part1 = Arduino Uno (Rev3)
  M1 = DC Motor
  M2 = DC Motor
  M3 = DC Motor
  M4 = DC Motor
  VCC1 = Battery block 9V

nets:
  N1: IC1.1_2EN, IC1.3_4EN, IC1.VCC1
  N2: IC1.1A, Part1.D10_PWM/SS
  N3: IC1.1Y, M2.pin_2, M4.pin_2
  GND1: IC1.GND1, IC1.GND2, IC1.GND3, IC1.GND4, VCC1.-
  N4: IC1.2Y, M2.pin_1, M4.pin_1
  N5: IC1.2A, Part1.D11_PWM/MOSI
  N6: IC1.VCC2, VCC1.+
  N7: IC1.3A, Part1.D9_PWM
  N8: IC1.3Y, M1.pin_2, M3.pin_2
  N9: IC1.4Y, M1.pin_1, M3.pin_1
  N10: IC1.4A, Part1.D8

notes:
  Bluetooth-Serial Module HC06
  VCC
  GND
  RXD
  TXD
