# Fritzing sketch id2018_16x2_I2C_LCD_0 (saved by Fritzing 0.9.3b)
circuit board: 8.46667cm x 5.64444cm
breadboards: 1

parts:
  DOWN = Pushbutton [package="[THT]"]
  UP = Pushbutton [package="[THT]"]
  Part1 = Arduino Nano (Rev3.0)
  part = Camdenboss CTB0158-4 [package=THT]

nets:
  N1: DOWN.Pin_1, DOWN.Pin_2, UP.Pin_1, UP.Pin_2, Part1.GND, part.pin4
  N2: DOWN.Pin_3, DOWN.Pin_4, Part1.D3
  N3: UP.Pin_3, UP.Pin_4, Part1.D2
  N4: Part1.5V, part.pin3
  N5: Part1.A5, part.pin1
  N6: Part1.A4, part.pin2

notes:
  I2C LCD
  GND
  VCC
  SDA
  SCL
