# Fritzing sketch id2019_is2_arduino_gogo_0 (saved by Fritzing 0.9.0b)

parts:
  J1 = screw terminal, 3 pins
  Componente1 = Arduino Uno (Rev3)
  J2 = screw terminal, 3 pins  # not connected

nets:
  N1: J1.pin1, Componente1.GND
  N2: J1.pin2, Componente1.A5/SCL
  N3: J1.pin3, Componente1.A4/SDA

notes:
  Conexão BR-GoGo Conectores I2C
