# Fritzing sketch id2022_I2C_OLED_button_fritzing_0 (saved by Fritzing 0.9.3b)
breadboards: 1

parts:
  Grove1 = Grove OLED 128x96
  부품1 = Arduino Uno (Rev3)
  S1 = Momentary Switch [package=ksa_sealed_tac_switch]
  R1 = Resistor [tolerance=±5% resistance=220 package=THT]

nets:
  GND: Grove1.GND, 부품1.GND, R1.Pin_0
  VCC: Grove1.VCC, 부품1.5V, S1.1
  N1: Grove1.SDA, 부품1.A4/SDA
  N2: Grove1.SCL, 부품1.A5/SCL
  N3: 부품1.D7, S1.3, R1.Pin_1
