# Fritzing sketch id2023_I2C_OLED_fritzing_0 (saved by Fritzing 0.9.3b)
breadboards: 1

parts:
  Grove1 = Grove OLED 128x96
  부품1 = Arduino Uno (Rev3)

nets:
  GND: Grove1.GND, 부품1.GND
  VCC: Grove1.VCC, 부품1.5V
  N1: Grove1.SDA, 부품1.A4/SDA
  N2: Grove1.SCL, 부품1.A5/SCL
