# Fritzing sketch id2024_Range_Expander_0 (saved by Fritzing 0.7.1b)
breadboards: 1

parts:
  IC2 = DIP___16_pins
  Arduino_I2C-Portexpander_V1_0 = Arduino
  R1 = Resistor [tolerance=±5% resistance=10k package=THT]
  J1 = female pin header, 4 pins [form="♀ (female)"]
  J2 = female pin header, 4 pins [form="♀ (female)"]
  IC3 = DIP___16_pins
  J3 = female pin header, 4 pins [form="♀ (female)"]
  J4 = female pin header, 4 pins [form="♀ (female)"]
  IC4 = DIP___16_pins
  J5 = female pin header, 4 pins [form="♀ (female)"]
  J6 = female pin header, 4 pins [form="♀ (female)"]

nets:
  N1: IC2.connector0, IC2.connector1, IC2.connector2, IC2.connector7, Arduino_I2C-Portexpander_V1_0.GND, IC3.connector1, IC3.connector2, IC3.connector7, IC4.connector0, IC4.connector2, IC4.connector7
  N2: IC2.connector3, J1.pin1
  N3: IC2.connector4, J1.pin2
  N4: IC2.connector5, J1.pin3
  N5: IC2.connector6, J1.pin4
  N6: IC2.connector8, J2.pin4
  N7: IC2.connector9, J2.pin3
  N8: IC2.connector10, J2.pin2
  N9: IC2.connector11, J2.pin1
  N10: IC2.connector12, Arduino_I2C-Portexpander_V1_0.A3, R1.Pin_1, IC3.connector12, IC4.connector12
  N11: IC2.connector13, Arduino_I2C-Portexpander_V1_0.A5, IC3.connector13, IC4.connector13
  N12: IC2.connector14, Arduino_I2C-Portexpander_V1_0.A4, IC3.connector14, IC4.connector14
  N13: IC2.connector15, Arduino_I2C-Portexpander_V1_0.+5V, R1.Pin_0, IC3.connector0, IC3.connector15, IC4.connector1, IC4.connector15
  N14: IC3.connector3, J3.pin1
  N15: IC3.connector4, J3.pin2
  N16: IC3.connector5, J3.pin3
  N17: IC3.connector6, J3.pin4
  N18: IC3.connector8, J4.pin4
  N19: IC3.connector9, J4.pin3
  N20: IC3.connector10, J4.pin2
  N21: IC3.connector11, J4.pin1
  N22: IC4.connector3, J5.pin1
  N23: IC4.connector4, J5.pin2
  N24: IC4.connector5, J5.pin3
  N25: IC4.connector6, J5.pin4
  N26: IC4.connector8, J6.pin4
  N27: IC4.connector9, J6.pin3
  N28: IC4.connector10, J6.pin2
  N29: IC4.connector11, J6.pin1
