# Fritzing sketch id2025_Z_Uno_bmp180_oled_0 (saved by Fritzing 0.9.2b)
breadboards: 1

parts:
  Z-uno_2_1 = zuno2
  Squix1 = OLED_SSD1306_I2C_128x64

nets:
  N1: Z-uno_2_1.connector3, Squix1.connector2
  N2: Z-uno_2_1.connector4, Squix1.connector1
  N3: Z-uno_2_1.connector15, Z-uno_2_1.connector16
  N4: Z-uno_2_1.connector17, Z-uno_2_1.connector18, Squix1.connector3
  N5: Z-uno_2_1.connector19, Squix1.connector4
  N6: Z-uno_2_1.connector41, Z-uno_2_1.connector44
  N7: Z-uno_2_1.connector42, Z-uno_2_1.connector43
