# Fritzing sketch id2026_I2C_Raspberry2_Arduino_0 (saved by Fritzing 0.9.2b)
breadboards: 1

parts:
  Raspberry_Pi1 = Raspberry Pi 2
  Componente1 = Arduino Uno (Rev3)
  Componente2 = Arduino Uno (Rev3)
  R1 = Resistor [tolerance=±5% resistance=100k package="2010 [SMD]"]
  R2 = Resistor [tolerance=±5% resistance=100k package="2010 [SMD]"]

nets:
  N1: Raspberry_Pi1.3v3, R1.Pin_0, R2.Pin_0
  N2: Raspberry_Pi1.GPIO2, Componente1.A4/SDA, Componente2.A4/SDA, R2.Pin_1
  N3: Raspberry_Pi1.GPIO3, Componente1.A5/SCL, Componente2.A5/SCL, R1.Pin_1
  GND: Raspberry_Pi1.GND, Componente1.GND, Componente2.GND

notes:
  R1 = R1 = 100K
  +3.3 V
  GND
  SDA
  SCL
