# Fritzing sketch id2027_CustomSevenSegment_0 (saved by Fritzing 0.9.2b)
breadboards: 1

parts:
  R1 = Resistor [tolerance=±10% resistance=330 package=THT]
  R2 = Resistor [tolerance=±10% resistance=330 package=THT]
  R3 = Resistor [tolerance=±10% resistance=330 package=THT]
  R4 = Resistor [tolerance=±10% resistance=330 package=THT]
  R5 = Resistor [tolerance=±10% resistance=330 package=THT]
  R6 = Resistor [tolerance=±10% resistance=330 package=THT]
  R7 = Resistor [tolerance=±10% resistance=330 package=THT]
  R8 = Resistor [tolerance=±10% resistance=330 package=THT]
  U2 = 74HC595 [package="DIP16 [THT]"]
  XTAL1 = Crystal [frequency="16 Mhz" package=THT]
  R9 = Resistor [tolerance=±5% resistance=2.2k package=THT]
  R10 = Resistor [tolerance=±5% resistance=2.2k package=THT]
  R11 = Resistor [tolerance=±5% resistance=2.2k package=THT]
  R12 = Resistor [tolerance=±5% resistance=2.2k package=THT]
  S1 = Momentary Switch [package=ksa_sealed_tac_switch]
  R13 = Resistor [tolerance=±5% resistance=1.5k package=THT]
  R14 = Resistor [tolerance=±5% resistance=1.5k package=THT]
  C1 = Ceramic Capacitor [capacitance=10pF package="0603 [SMD, multilayer]"]
  C2 = Ceramic Capacitor [capacitance=10pF package="0603 [SMD, multilayer]"]
  7_Segment5 = 7 Segment Display
  7_Segment6 = 7 Segment Display
  7_Segment7 = 7 Segment Display
  7_Segment8 = 7 Segment Display
  U1 = atmega168 [package=dip]
  Q1 = PNP-Transistor [part_number=S8550 package="TO92 [THT]"]
  Q2 = PNP-Transistor [part_number=S8550 package="TO92 [THT]"]
  Q3 = PNP-Transistor [part_number=S8550 package="TO92 [THT]"]
  Q4 = PNP-Transistor [part_number=S8550 package="TO92 [THT]"]

nets:
  N1: R1.Pin_0, 7_Segment5.Segment_F, 7_Segment6.Segment_F, 7_Segment7.Segment_F, 7_Segment8.Segment_F
  N2: R1.Pin_1, U2.Q5
  N3: R2.Pin_0, 7_Segment5.Segment_A, 7_Segment6.Segment_A, 7_Segment7.Segment_A, 7_Segment8.Segment_A
  N4: R2.Pin_1, U2.Q6
  N5: R3.Pin_0, 7_Segment5.Segment_B, 7_Segment6.Segment_B, 7_Segment7.Segment_B, 7_Segment8.Segment_B
  N6: R3.Pin_1, U2.Q7
  N7: R4.Pin_0, 7_Segment5.Segment_G, 7_Segment6.Segment_G, 7_Segment7.Segment_G, 7_Segment8.Segment_G
  N8: R4.Pin_1, U2.Q4
  N9: R5.Pin_0, 7_Segment5.Segment_DP, 7_Segment6.Segment_DP, 7_Segment7.Segment_DP, 7_Segment8.Segment_DP
  N10: R5.Pin_1, U2.Q0
  N11: R6.Pin_0, 7_Segment5.Segment_C, 7_Segment6.Segment_C, 7_Segment7.Segment_C, 7_Segment8.Segment_C
  N12: R6.Pin_1, U2.Q1
  N13: R7.Pin_0, 7_Segment5.Segment_D, 7_Segment6.Segment_D, 7_Segment7.Segment_D, 7_Segment8.Segment_D
  N14: R7.Pin_1, U2.Q2
  N15: R8.Pin_0, 7_Segment5.Segment_E, 7_Segment6.Segment_E, 7_Segment7.Segment_E, 7_Segment8.Segment_E
  N16: R8.Pin_1, U2.Q3
  N17: U2.MR, R14.Pin_1, U1.VCC, U1.AVCC
  N18: U2.SH_CP, U1.D10_(PWM)
  N19: U2.ST_CP, U1.D8
  N20: U2.OE, S1.1, C1.0, C2.1, U1.GND, Q1.E, Q2.E, Q3.E
  N21: U2.DS, U1.D9_(PWM)
  N22: XTAL1.pin_0, C2.0, U1.XLAT2
  N23: XTAL1.pin_1, C1.1, U1.XLAT1
  N24: R9.Pin_0, Q2.B
  N25: R9.Pin_1, U1.D4
  N26: R10.Pin_0, Q1.B
  N27: R10.Pin_1, U1.D5_(PWM)
  N28: R11.Pin_0, Q4.B
  N29: R11.Pin_1, U1.D2
  N30: R12.Pin_0, Q3.B
  N31: R12.Pin_1, U1.D3_(PWM)
  N32: S1.3, U1.RESET
  N33: R13.Pin_0, U1.A5
  N34: R14.Pin_0, U1.A4
  N35: 7_Segment5.common_anode, Q1.C
  N36: 7_Segment6.common_anode, Q2.C
  N37: 7_Segment7.common_anode, Q3.C
  N38: 7_Segment8.common_anode, Q4.C
