# Fritzing sketch id2028_7_segment_LED_0 (saved by Fritzing 0.9.2b)
breadboards: 1

parts:
  U1 = attiny85 [package=dip]
  U3 = 7-SEGMENT-4DIGIT [package=7-segment-4digit_longpads_for_pogobed]  # not connected
  U4 = Header 4 [package=1x04-smd]
  R1 = PHOTOCELL [package=photocell]
  R2 = Resistor [tolerance=±5% resistance=1k package=THT]

nets:
  N1: U1.Pin_3, R1.P$2, R2.Pin_0
  N2: U1.Pin_4, U4.2, R2.Pin_1
  N3: U1.Pin_5, U4.3
  N4: U1.Pin_7, U4.4
  N5: U1.Pin_8, U4.1, R1.P$1
