# Fritzing sketch id2029_iBlood_0 (saved by Fritzing 0.9.2b)
circuit board: 8.46667cm x 5.64444cm

parts:
  Součástka1 = Arduino Uno (Rev3)
  U1 = DCM01 Reflective Blood Sensor [package=dcm01]
  Power_plug1 = Power plug
  Součástka2 = Thermal Printer

nets:
  N1: Součástka1.A1, U1.4
  N2: Součástka1.D5_PWM, Součástka2.TXD
  N3: Součástka1.D6_PWM, Součástka2.RXD
  N4: Součástka1.5V, U1.1
  N5: Součástka1.GND, U1.2, Součástka2.GND#2
  N6: Power_plug1.VCC, Součástka2.VH

notes:
  5V / 2A
