# Fritzing sketch id2032_CL_8038_gerador_de_formas_de_onda._0 (saved by Fritzing 0.9.3b)
circuit board: 4.14916cm x 8.92253cm
perfboards: 1

parts:
  U1 = prefix0000
  R5 = Resistor [tolerance=±5% resistance=15k package=THT]
  OUTPUT = female pin header, 3 pins [form="♀ (female)"]
  R8 = Resistor [tolerance=±5% resistance=20k package=THT]
  R6 = Resistor [tolerance=±5% resistance=4.7k package=THT]
  D2 = P1000K [part_number=1B457]
  R2 = Resistor [tolerance=±5% resistance=4.7k package=THT]
  C3 = Electrolytic Capacitor [capacitance=4.7mF package="100 mil [THT, electrolytic]"]
  POWER = female pin header, 2 pins [form="♀ (female)"]
  R9 = Rotary Potentiometer (Large) [maximum_resistance=100k package=THT]
  R7 = Rotary Potentiometer (Large) [maximum_resistance=15M package=THT]
  R6_2 = Rotary Potentiometer (Large) [maximum_resistance=15M package=THT]
  R4 = Rotary Potentiometer (Large) [maximum_resistance=100k package=THT]
  R1 = Electrolytic Capacitor [capacitance=0.1µF package="100 mil [THT, electrolytic]"]

nets:
  N1: U1.connector1, OUTPUT.pin3
  N2: U1.connector2, OUTPUT.pin2
  N3: U1.connector3, R2.Pin_0
  N4: U1.connector4, R6.Pin_0, R7.leg2
  N5: U1.connector5, D2.cathode, R4.wiper
  N6: U1.connector7, R6_2.wiper, R1.-
  N7: U1.connector8, R5.Pin_0, OUTPUT.pin1
  N8: U1.connector9, C3.+
  N9: U1.connector10, R8.Pin_0, C3.-, R7.leg1
  N10: U1.connector11, R9.leg2
  10V: R5.Pin_1, D2.anode, POWER.pin1, R6_2.leg2, R1.+
  N11: R8.Pin_1, R6_2.leg1
  N12: R6.Pin_1, R4.leg2
  N13: R2.Pin_1, R4.leg1
  GND: POWER.pin2, R9.leg1, R9.wiper

notes:
  CL8038, 1
  MOSELEY MIRANDA GOES
  O diagrama de circuito fornecido mostra um oscilador de freqüência de áudio variável usando ICL8038. Esse circuito é muito útil ao testar projetos relacionados ao áudio. A faixa de frequência deste circuito é de 20Hz a 20KHz. POT R6 pode ser usado para ajustar a freqüência enquanto POT R9 pode ser usado para ajustar a distorção. POT R4 pode ser usado para ajustar o ciclo de trabalho, enquanto o POT R7 pode ser usado para anular as variações no ciclo de trabalho. C2 é o capacitor de temporização externo e R5 é um resistor de pull up.
  MOSELEY MIRANDA
  Gerador de formas de onda
