# Fritzing sketch id2033_IRdump_0 (saved by Fritzing 0.9.2b)

parts:
  IR1 = TSOP312.., 314.. [package=THT]
  Componente1 = Arduino Uno (Rev3) - ICSP

nets:
  N1: IR1.GND, Componente1.ICSP_MOSI, Componente1.D11_PWM/MOSI
  N2: IR1.Vs, Componente1.GND
  N3: IR1.Data, Componente1.3V3

notes:
  Receiver IR model unknow but packaging have this code (342)
