# Fritzing sketch id2035_Ideal_Joystick_II_SIly4N0_0 (saved by Fritzing 0.9.3b)
breadboards: 1

parts:
  PDL1 = Slide Potentiometer [maximum_resistance=100kΩ]
  PDL0 = Slide Potentiometer [maximum_resistance=100kΩ]
  X1 = DB9 Connector [package=db9]
  Up = D2F_FL_Omron_Snap_Action_Limit_Switch_with_Level
  Down = D2F_FL_Omron_Snap_Action_Limit_Switch_with_Level
  Right = D2F_FL_Omron_Snap_Action_Limit_Switch_with_Level
  Left = D2F_FL_Omron_Snap_Action_Limit_Switch_with_Level
  R3 = Resistor [tolerance=±5% resistance=680 package=THT]
  R4 = Resistor [tolerance=±5% resistance=680 package=THT]
  SW1 = Round Pushbutton
  SW0 = Round Pushbutton
  R5 = Resistor [tolerance=±5% resistance=680 package=THT]
  Fire = Toggle Switch [package=THT]
  R6 = Resistor [tolerance=±5% resistance=680 package=THT]
  R7 = Resistor [tolerance=±5% resistance=180k package=THT]
  R8 = Resistor [tolerance=±5% resistance=180k package=THT]

nets:
  N1: PDL1.leg1, PDL0.leg1, X1.2, Up.connector1pad_1, Left.connector1pad_1, SW1.leg1, Fire.L1
  N2: PDL1.wiper, R3.Pin_0
  N3: PDL0.wiper, R4.Pin_0
  N4: X1.1, SW1.leg0, R5.Pin_0
  N5: X1.3, Down.connector1pad_1, Right.connector1, R5.Pin_1, R6.Pin_1, R7.Pin_0, R8.Pin_0
  N6: X1.5, Right.connector1pad_1, Left.connector1, R4.Pin_1, R8.Pin_1
  N7: X1.7, SW0.leg0, R6.Pin_0
  N8: X1.8, Up.connector1, Down.connector1, R3.Pin_1, R7.Pin_1
  N9: SW0.leg1, Fire.COM
