# Fritzing sketch id2036_IDP_circuit_0 (saved by Fritzing 0.9.3b)
stripboards: 1

parts:
  R1 = Trimmer Potentiometer [maximum_resistance=10kΩ package=THT]
  Q1 = PHOTOTRANSISTOR REFLECTIVE OBJECT SENSOR [package=qrb1114-side]
  R2 = Trimmer Potentiometer [maximum_resistance=10kΩ package=THT]
  R4 = Resistor [tolerance=±5% resistance=220 package=THT]
  VCC1 = Battery
  U1 = LM 358 Dual Op-Amp [package="DIP8 [THT]"]
  R5 = Trimmer Potentiometer [maximum_resistance=10kΩ package=THT]
  R6 = Resistor [tolerance=±5% resistance=220 package=THT]
  R3 = Resistor [tolerance=±5% resistance=220 package=THT]
  R7 = Resistor [tolerance=±5% resistance=220 package=THT]

nets:
  N1: R1.leg1, Q1.K, VCC1.-, U1.connector3, U1.connector4, R5.leg2, R7.Pin_1
  N2: R1.wiper, Q1.A
  N3: R1.leg2, R2.leg1, VCC1.+, U1.connector0, U1.connector7, R5.leg1, R6.Pin_0
  N4: Q1.C, R4.Pin_0
  N5: Q1.E, R2.wiper
  N6: R2.leg2, R3.Pin_0
  N7: R4.Pin_1, U1.connector2, U1.connector5, R7.Pin_0
  N8: U1.connector1, U1.connector6, R5.wiper, R6.Pin_1
