# Fritzing sketch id2037_IDP_circuit_0 (saved by Fritzing 0.9.3b)
stripboards: 1

parts:
  R1 = Trimmer Potentiometer [maximum_resistance=10kΩ package=THT]
  Q1 = PHOTOTRANSISTOR REFLECTIVE OBJECT SENSOR [package=qrb1114-side]
  R2 = Trimmer Potentiometer [maximum_resistance=10kΩ package=THT]
  R4 = Resistor [tolerance=±5% resistance=220 package=THT]
  VCC1 = Battery
  U1 = LM 358 Dual Op-Amp [package="DIP8 [THT]"]
  R5 = Trimmer Potentiometer [maximum_resistance=10kΩ package=THT]
  R6 = Resistor [tolerance=±5% resistance=220 package=THT]
  R3 = Resistor [tolerance=±5% resistance=220 package=THT]
  R7 = Resistor [tolerance=±5% resistance=220 package=THT]
  3-pins_Hall_Effect_Sensor1 = mystery part, 3 pins [chip_label="Hall Effect Sensor"]
  U2 = LM 358 Dual Op-Amp [package="DIP8 [THT]"]
  R8 = Resistor [tolerance=±5% resistance=220 package=THT]
  R9 = Trimmer Potentiometer [maximum_resistance=10kΩ package=THT]
  R10 = Resistor [tolerance=±5% resistance=220 package=THT]
  LED1 = LED - 5mm [color="Red (633nm)" package="5 mm [THT]"]
  R11 = Resistor [tolerance=±5% resistance=220 package=THT]
  R12 = Trimmer Potentiometer [maximum_resistance=10kΩ package=THT]
  R13 = Resistor [tolerance=±5% resistance=220 package=THT]
  LED2 = LED - 5mm [color="Red (633nm)" package="5 mm [THT]"]

nets:
  N1: R1.leg1, Q1.K, VCC1.-, U1.connector3, R5.leg2, R7.Pin_1, 3-pins_Hall_Effect_Sensor1.pin1, LED1.cathode, LED2.anode
  N2: R1.wiper, Q1.A
  N3: R1.leg2, R2.leg1, VCC1.+, U1.connector7, R5.leg1, 3-pins_Hall_Effect_Sensor1.pin3, R8.Pin_0, R11.Pin_0
  N4: Q1.C, R4.Pin_0
  N5: Q1.E, R2.wiper
  N6: R2.leg2, R3.Pin_0
  N7: R4.Pin_1, U1.connector2, R7.Pin_0
  N8: U1.connector0, R6.Pin_0
  N9: U1.connector1, R5.wiper, R6.Pin_1
  N10: 3-pins_Hall_Effect_Sensor1.pin2, U2.connector2, U2.connector5
  N11: U2.connector0, U2.connector7, LED1.anode
  N12: U2.connector1, U2.connector6, R9.wiper, LED2.cathode
  N13: U2.connector3, U2.connector4, R12.wiper
  N14: R8.Pin_1, R9.leg1
  N15: R9.leg2, R10.Pin_0
  N16: R11.Pin_1, R12.leg2
  N17: R12.leg1, R13.Pin_0
