# Fritzing sketch id2038_arduino_wiering1_0 (saved by Fritzing 0.9.2b)
breadboards: 1

parts:
  S1 = Pushbutton [package="[THT]"]
  J1 = Basic Servo
  Part1 = Arduino Uno (Rev3)
  R1 = Resistor [tolerance=±5% resistance=220 package=THT]
  S2 = Pushbutton [package="[THT]"]
  R2 = Resistor [tolerance=±5% resistance=220 package=THT]
  S3 = Pushbutton [package="[THT]"]
  R3 = Resistor [tolerance=±5% resistance=220 package=THT]
  L1 = Solenoid
  Q1 = Basic FET P-Channel [package="TO220 [THT]"]
  R4 = Resistor [tolerance=±5% resistance=220 package=THT]
  VCC1 = Battery
  D1 = Rectifier Diode [part_number=1N4001 package="300 mil [THT]"]
  L2 = Solenoid
  Q2 = Basic FET P-Channel [package="TO220 [THT]"]
  R5 = Resistor [tolerance=±5% resistance=220 package=THT]
  D2 = Rectifier Diode [part_number=1N4001 package="300 mil [THT]"]
  L3 = Solenoid
  Q3 = Basic FET P-Channel [package="TO220 [THT]"]
  D3 = Rectifier Diode [part_number=1N4001 package="300 mil [THT]"]
  R6 = Resistor [tolerance=±5% resistance=220 package=THT]

nets:
  N1: S1.Pin_1, S1.Pin_2, Part1.D2, R1.Pin_0
  GND: S1.Pin_3, S1.Pin_4, J1.gnd, Part1.GND, S3.Pin_3, S3.Pin_4, L1.pin1, Q1.source, VCC1.-, L3.pin1, L3.pin2, Q3.source
  VCC: J1.vcc, Part1.5V, R1.Pin_1, R2.Pin_1
  N2: J1.pulse, Part1.D11_PWM/MOSI
  N3: Part1.D8, S3.Pin_1, S3.Pin_2, R3.Pin_0
  N4: Part1.D9_PWM, R6.Pin_0
  N5: Part1.D13/SCK, R4.Pin_0
  N6: Part1.D7, S2.Pin_1, S2.Pin_2, R2.Pin_0
  N7: S2.Pin_3, S2.Pin_4
  N8: L1.pin2, VCC1.+, D1.cathode, L2.pin2, D2.cathode, D3.cathode
  N9: Q1.gate, R4.Pin_1
  N10: Q1.drain, D1.anode
  N11: L2.pin1, Q2.source
  N12: Q2.gate, R5.Pin_1
  N13: Q2.drain, D2.anode
  N14: Q3.gate, R6.Pin_1
  N15: Q3.drain, D3.anode
