# Fritzing sketch id203_SWITCH_LEDS_ON_OFF_AX801F6_0 (saved by Fritzing 0.9.3b)
circuit board: 8.46667cm x 5.64444cm
breadboards: 1

parts:
  Part1 = Arduino Uno (Rev3)
  LED1 = LED - 5mm [color="Red (633nm)" package="5 mm [THT]"]  # not connected
  LED2 = LED - 5mm [color="Green (570nm)" package="5 mm [THT]"]
  LED3 = LED - 5mm [color="Yellow (592nm)" package="5 mm [THT]"]
  LED4 = LED - 5mm [color="Blue (525nm)" package="5 mm [THT]"]
  S1 = Pushbutton [package="[THT]"]
  R1 = Resistor [tolerance=±5% resistance=220 package=THT]
  R2 = Resistor [tolerance=±5% resistance=220 package=THT]
  R3 = Resistor [tolerance=±5% resistance=220 package=THT]
  R4 = Resistor [tolerance=±5% resistance=220 package=THT]
  R5 = Resistor [tolerance=±5% resistance=10k package=THT]
  R6 = Resistor [tolerance=±5% resistance=100 package=THT]

nets:
  N1: Part1.D8, R5.Pin_1
  N2: Part1.D10_PWM/SS, LED4.cathode
  N3: Part1.D11_PWM/MOSI, LED3.cathode
  N4: Part1.D12/MISO, LED2.cathode
  N5: Part1.GND, S1.Pin_3, S1.Pin_4, R1.Pin_0, R2.Pin_0, R3.Pin_0, R4.Pin_0, R6.Pin_1
  N6: LED2.anode, R2.Pin_1
  N7: LED3.anode, R3.Pin_1
  N8: LED4.anode, R4.Pin_1
  N9: S1.Pin_1, S1.Pin_2, R5.Pin_0, R6.Pin_0

notes:
  Made using a clone arduino with ch34x Serial - https://www.amazon.co.uk/gp/product/B00SR4FLMI/ref=oh_aui_detailpage_o02_s00?ie=UTF8&psc=1
  Uses part of button tutorial from http://www.ladyada.net/learn/arduino/lesson5.html
  Also uses the Bounce2 debouncing library - https://github.com/thomasfredericks/Bounce2
