# Fritzing sketch id2040_ifractal_leo_shield_rev4_0 (saved by Fritzing 0.9.2b)
circuit board: 6.88566cm x 5.36311cm
breadboards: 1

parts:
  4081_AND = SN74LS20N [package="DIP14 [THT]"]
  Teclado_4x4 = female pin header, 9 pins [form="♀ (female)"]
  RFID_Saida = female pin header, 6 pins [form="♀ (female)"]
  RFID_Cofre = female pin header, 6 pins [form="♀ (female)"]
  RFID_Entrada = female pin header, 6 pins [form="♀ (female)"]
  Cofre = female pin header, 4 pins [form="♀ (female)"]
  Sensores = female pin header, 6 pins [form="♀ (female)"]
  Pictograma = female pin header, 6 pins [form="♀ (female)"]
  R3 = Resistor [tolerance=±5% resistance=220 package=THT]
  R4 = Resistor [tolerance=±5% resistance=220 package=THT]
  R5 = Resistor [tolerance=±5% resistance=220 package=THT]
  R6 = Resistor [tolerance=±5% resistance=220 package=THT]
  Buzzer = female pin header, 2 pins [form="♀ (female)"]
  R7 = Resistor [tolerance=±5% resistance=220 package=THT]
  7400_NAND = SN74LS20N [package="DIP14 [THT]"]
  Trava = female pin header, 4 pins [form="♀ (female)"]
  Leo_Shield = Arduino Leonardo (Rev3b)
  GND_TX_RX = female pin header, 4 pins [form="♀ (female)"]
  Display = female pin header, 11 pins [form="♀ (female)"]
  GND_IO_Vcc = female pin header, 4 pins [form="♀ (female)"]
  SPI_Header = double row male pin header, 6 pins [form="♂ (male)"]

nets:
  N1: 4081_AND.1A, Teclado_4x4.pin6, Leo_Shield.D9_PWM/A9, Display.pin3
  N2: 4081_AND.1B, 4081_AND.1D, 4081_AND.2A, 4081_AND.2D, Leo_Shield.D12/A11
  N3: 4081_AND.NC#2, Buzzer.pin1
  N4: 4081_AND.1C, Cofre.pin2
  N5: 4081_AND.1Y, Teclado_4x4.pin4, Leo_Shield.D8/A8, Display.pin2
  GND: 4081_AND.GND, RFID_Saida.pin6, RFID_Cofre.pin6, RFID_Entrada.pin6, Cofre.pin1, Pictograma.pin6, R3.Pin_1, R4.Pin_1, R5.Pin_0, R6.Pin_0, R7.Pin_0, 7400_NAND.GND, Trava.pin1, Leo_Shield.GND, GND_TX_RX.pin4, Display.pin6, Display.pin8, Display.pin11, GND_IO_Vcc.pin4
  N6: 4081_AND.2Y, Teclado_4x4.pin9, Leo_Shield.D10_PWM/A10, Display.pin4
  N7: 4081_AND.2B, Pictograma.pin2
  N8: 4081_AND.NC#10, Pictograma.pin3
  N9: 4081_AND.2C, Teclado_4x4.pin1, Leo_Shield.D11_PWM, Display.pin1
  VCC: 4081_AND.VCC, RFID_Saida.pin1, RFID_Cofre.pin1, RFID_Entrada.pin1, Cofre.pin4, Sensores.pin1, Pictograma.pin1, 7400_NAND.VCC, Trava.pin4, Leo_Shield.5V, Display.pin9, GND_IO_Vcc.pin1
  N10: Teclado_4x4.pin2, Leo_Shield.A2
  N11: Teclado_4x4.pin3, Leo_Shield.A3
  N12: Teclado_4x4.pin5, Leo_Shield.A4
  N13: Teclado_4x4.pin7, Leo_Shield.A5
  N14: RFID_Saida.pin3, 7400_NAND.1C
  N15: RFID_Saida.pin4, 7400_NAND.1D, 7400_NAND.2C
  N16: RFID_Cofre.pin3, 7400_NAND.2B
  N17: RFID_Cofre.pin4, 7400_NAND.2A, Leo_Shield.D6_PWM/A7
  N18: RFID_Entrada.pin3, 7400_NAND.1A
  N19: RFID_Entrada.pin4, 7400_NAND.1B, 7400_NAND.2D
  N20: Sensores.pin2, R5.Pin_1, Leo_Shield.A0
  N21: Sensores.pin4, R3.Pin_0
  N22: Sensores.pin5, R6.Pin_1, Leo_Shield.A1
  N23: Sensores.pin6, R4.Pin_0
  N24: Buzzer.pin2, R7.Pin_1
  N25: 7400_NAND.NC#2, Leo_Shield.D2/SDA
  N26: 7400_NAND.1Y, Leo_Shield.D3_PWM/SCL
  N27: 7400_NAND.2Y, Leo_Shield.D7
  N28: 7400_NAND.NC#10, Leo_Shield.D5_PWM
  N29: Trava.pin2, Leo_Shield.D13_PWM
  N30: Leo_Shield.D0/RX, GND_TX_RX.pin1
  N31: Leo_Shield.D1/TX, GND_TX_RX.pin2
  N32: Leo_Shield.D4/A6, GND_IO_Vcc.pin3
  N33: Display.pin5, SPI_Header.pin2
  N34: Display.pin7, SPI_Header.pin1
