# Fritzing sketch id2041_ifractal_mega_extra_shield_0 (saved by Fritzing 0.9.2b)
circuit board: 3.86291cm x 5.66913cm
breadboards: 1

parts:
  Pictograma2 = double row female pin header, 36 pins [form="♀ (female)"]
  Pictograma3 = female pin header, 8 pins [form="♀ (female)"]
  Display = female pin header, 11 pins [form="♀ (female)"]
  Teclado_4x4 = female pin header, 9 pins [form="♀ (female)"]
  RFID_Saida = female pin header, 6 pins [form="♀ (female)"]
  Pictograma1 = female pin header, 8 pins [form="♀ (female)"]
  7400_NAND = SN74LS20N [package="DIP14 [THT]"]
  RFID_Entrada = female pin header, 6 pins [form="♀ (female)"]
  5v = female pin header, 2 pins [form="♀ (female)"]
  Vcc_TX_RX_GND = female pin header, 5 pins [form="♀ (female)"]
  Vcc_TX_RX_GND_2 = female pin header, 5 pins [form="♀ (female)"]
  GND_RX_TX_Vcc = female pin header, 5 pins [form="♀ (female)"]
  MI_SCK_SS_MO = female pin header, 4 pins [form="♀ (female)"]

nets:
  N1: Pictograma2.pin1, RFID_Saida.pin6, 7400_NAND.VCC, RFID_Entrada.pin1, Vcc_TX_RX_GND.pin5, Vcc_TX_RX_GND_2.pin5
  N2: Pictograma2.pin11, 7400_NAND.2Y
  N3: Pictograma2.pin12, Teclado_4x4.pin9
  N4: Pictograma2.pin13, Teclado_4x4.pin6
  N5: Pictograma2.pin14, Teclado_4x4.pin4
  N6: Pictograma2.pin15, Teclado_4x4.pin1
  N7: Pictograma2.pin16, MI_SCK_SS_MO.pin1
  N8: Pictograma2.pin17, MI_SCK_SS_MO.pin2
  N9: Pictograma2.pin18, RFID_Saida.pin1, 7400_NAND.GND, RFID_Entrada.pin6, Vcc_TX_RX_GND.pin1, Vcc_TX_RX_GND_2.pin1
  N10: Pictograma2.pin19, Display.pin11, GND_RX_TX_Vcc.pin5
  N11: Pictograma2.pin20, MI_SCK_SS_MO.pin3
  N12: Pictograma2.pin21, MI_SCK_SS_MO.pin4
  N13: Pictograma2.pin22, Display.pin8
  N14: Pictograma2.pin23, Display.pin7
  N15: Pictograma2.pin24, Display.pin6
  N16: Pictograma2.pin25, Display.pin5
  N17: Pictograma2.pin26, Display.pin4
  N18: Pictograma2.pin27, Display.pin3
  N19: Pictograma2.pin28, Display.pin2
  N20: Pictograma2.pin29, Display.pin1
  N21: Pictograma2.pin36, Display.pin9, 5v.pin1
  N22: Pictograma3.pin1, Teclado_4x4.pin7
  N23: Pictograma3.pin2, Teclado_4x4.pin5
  N24: Pictograma3.pin7, Teclado_4x4.pin3
  N25: Pictograma3.pin8, Teclado_4x4.pin2
  N26: RFID_Saida.pin3, 7400_NAND.1B, 7400_NAND.2A
  N27: RFID_Saida.pin4, 7400_NAND.1A
  N28: Pictograma1.pin1, Vcc_TX_RX_GND_2.pin3
  N29: Pictograma1.pin2, Vcc_TX_RX_GND_2.pin2
  N30: Pictograma1.pin3, Vcc_TX_RX_GND.pin3
  N31: Pictograma1.pin4, Vcc_TX_RX_GND.pin2
  N32: Pictograma1.pin5, GND_RX_TX_Vcc.pin3
  N33: Pictograma1.pin6, GND_RX_TX_Vcc.pin4
  N34: Pictograma1.pin7, 7400_NAND.NC#2
  N35: Pictograma1.pin8, 7400_NAND.NC#10
  N36: 7400_NAND.2B, 7400_NAND.2C, RFID_Entrada.pin4
  N37: 7400_NAND.2D, RFID_Entrada.pin3
  N38: 5v.pin2, GND_RX_TX_Vcc.pin1

notes:
  jumper
  GND
  S3
  S2
  S1
