# Fritzing sketch id2042_Dioder_0 (saved by Fritzing 0.7.12b)
breadboards: 2

parts:
  Nano1 = Arduino Nano v2.3
  R1 = Resistor [tolerance=±5% resistance=100 package=THT]
  R2 = Resistor [tolerance=±5% resistance=100 package=THT]
  R3 = Resistor [tolerance=±5% resistance=100 package=THT]
  GREEN = LED - 3mm [color="Red (633nm)" package="3 mm [THT]"]
  BLUE = LED - 3mm [color="Red (633nm)" package="3 mm [THT]"]
  IC1 = ULN2003A [package="DIP16 [THT]"]
  RED = LED - 3mm [color="Red (633nm)" package="3 mm [THT]"]
  J3 = screw terminal, 5 pins
  J4 = screw terminal, 3 pins
  J1 = male pin header, 2 pins [form="♂ (male)"]

nets:
  GND: Nano1.GND, GREEN.cathode, BLUE.cathode, IC1.0V, RED.cathode, J3.pin5
  N1: Nano1.D3, R1.Pin_0, IC1.In_6
  N2: Nano1.D5, R2.Pin_0, IC1.In_5
  N3: Nano1.D6, R3.Pin_0, IC1.In_4
  N4: Nano1.D9, IC1.In_3
  N5: Nano1.D10, IC1.In_2
  N6: Nano1.D11, IC1.In_1
  12V: Nano1.VIN, IC1.COM_-_Common, J1.pin2
  N7: R1.Pin_1, IC1.Out_6, RED.anode, J4.pin3
  N8: R2.Pin_1, GREEN.anode
  N9: R3.Pin_1, BLUE.anode
  N10: IC1.Out_5, J4.pin1
  N11: IC1.Out_4, J4.pin2
  N12: IC1.Out_3, J3.pin4
  N13: IC1.Out_2, J3.pin2
  N14: IC1.Out_1, J3.pin3
  N15: J3.pin1, J1.pin1

notes:
  IKEA Dioder cable (Note the order)
  To Raspberry Pi
  RBG
  Dioder hack 0.1
  Martin Isaksson 2013
  Vin
  +
  GND
  Red
  Blue
  Green
  CH1
  CH2
  Designed in Sweden
