# Fritzing sketch id2043_ilintino_max1.1n_0 (saved by Fritzing 0.8.6b)
circuit board: 6.47228cm x 4.95957cm
breadboards: 2

parts:
  U1 = atmega328 [package=dip]
  J2 = female pin header, 5 pins [form="♀ (female)"]
  R3 = Resistor [tolerance=±5% resistance=680 package=THT]
  C5 = Electrolytic Capacitor [capacitance=0.47mF voltage=10V package="200 mil [THT, electrolytic]"]
  C6 = Electrolytic Capacitor [capacitance=0.1mF voltage=6.3V package="200 mil [THT, electrolytic]"]
  C7 = Tantalum Capacitor [capacitance=0.1µF package="200 mil [THT, tantalum]"]
  L2 = Inductor [part_number=22uH]
  max1 = DIP___8_pins
  J4 = female pin header, 8 pins [form="♀ (female)"]
  C8 = Tantalum Capacitor [capacitance="1 μF" voltage=10V package="100 mil [THT, tantalum]"]
  S1_RESET = Pushbutton [package="[THT]"]
  D3 = Schottky Diode [part_number=1N5817 package="300 mil [THT]"]
  J9 = female pin header, 2 pins [form="♀ (female)"]
  LED2_D9 = LED - 3mm [color="Red (633nm)" package="3 mm [THT]"]
  LED1_POWER = LED - 3mm [color="Green (570nm)" package="3 mm [THT]"]
  J10 = female pin header, 2 pins [form="♀ (female)"]
  LED3_TX = LED - 3mm [color="Orange (620nm)" package="3 mm [THT]"]
  LED4_RX = LED - 3mm [color="Yellow (595nm)" package="3 mm [THT]"]
  R5 = Resistor [tolerance=±5% resistance=680 package=THT]
  R4 = Resistor [tolerance=±5% resistance=680 package=THT]
  D2 = Schottky Diode [part_number=1N5817 package="300 mil [THT]"]
  J5 = female pin header, 6 pins [form="♀ (female)"]
  J6 = female pin header, 4 pins [form="♀ (female)"]
  R2 = Resistor [tolerance=±5% resistance=680 package=THT]
  R1 = Resistor [tolerance=±5% resistance=680 package=THT]

nets:
  N1: U1.RESET, S1_RESET.Pin_1, S1_RESET.Pin_2, R5.Pin_1, J5.pin1
  N2: U1.D0_(RX), J5.pin2, R1.Pin_1
  N3: U1.D1_(TX), J5.pin3, R2.Pin_1
  N4: U1.D2, J5.pin4
  N5: U1.D3_(PWM), J5.pin5
  N6: U1.D4, J5.pin6
  N7: U1.VCC, U1.AVCC, C5.+, max1.connector5, C8.+, J10.pin2, R5.Pin_0, R4.Pin_1, D2.cathode
  GND: U1.GND, C5.-, C6.-, C7.-, max1.connector1, max1.connector6, J4.pin7, C8.-, S1_RESET.Pin_3, S1_RESET.Pin_4, J9.pin1, LED2_D9.anode, LED1_POWER.anode, J10.pin1, LED3_TX.anode, LED4_RX.anode
  N8: U1.D5_(PWM), J6.pin1
  N9: U1.D6_(PWM), J6.pin2
  N10: U1.D7, J6.pin3
  N11: U1.D8, J6.pin4
  N12: U1.D9_(PWM), J2.pin5, R3.Pin_0
  N13: U1.D10_(PWM), J2.pin4
  N14: U1.D11_(PWM), J2.pin3
  N15: U1.D12, J2.pin2
  N16: U1.D13, J2.pin1
  N17: U1.AREF, J4.pin8
  N18: U1.A0, J4.pin6
  N19: U1.A1, J4.pin5
  N20: U1.A2, J4.pin4
  N21: U1.A3, J4.pin3
  N22: U1.A4, J4.pin2
  N23: U1.A5, J4.pin1
  N24: R3.Pin_1, LED2_D9.cathode
  N25: C6.+, L2.connector1, max1.connector0, max1.connector4, D3.cathode
  N26: C7.+, max1.connector2
  N27: L2.connector0, max1.connector7, D2.anode
  N28: D3.anode, J9.pin2
  N29: LED1_POWER.cathode, R4.Pin_0
  N30: LED3_TX.cathode, R2.Pin_0
  N31: LED4_RX.cathode, R1.Pin_0

notes:
  circuito base ilintino max
