# Fritzing sketch id2046_LED_Project_1_0 (saved by Fritzing 0.9.2b)
breadboards: 1

parts:
  VCC1 = Battery
  S1 = Pushbutton [package="[THT]"]
  R1 = Resistor [tolerance=±5% resistance=220 package=THT]
  R2 = Resistor [tolerance=±5% resistance=220 package=THT]
  LED1 = LED - 5mm [color="Red (633nm)" package="5 mm [THT]"]
  LED2 = LED - 5mm [color="Red (633nm)" package="5 mm [THT]"]

nets:
  N1: VCC1.-, S1.Pin_3, S1.Pin_4
  N2: VCC1.+, LED1.cathode, LED2.cathode
  N3: S1.Pin_1, S1.Pin_2, R1.Pin_0, R2.Pin_0
  N4: R1.Pin_1, LED1.anode
  N5: R2.Pin_1, LED2.anode
