# Fritzing sketch id2049_Impreso_0 (saved by Fritzing 0.7.4b)
breadboards: 1

parts:
  IC1 = L293D [package=THT]
  J1 = Screw terminal - 2 pins [package=THT]
  J2 = Screw terminal - 2 pins [package=THT]
  J3 = female pin header, 2 pins [form="♀ (female)"]
  J4 = female pin header, 2 pins [form="♀ (female)"]
  J5 = female pin header, 2 pins [form="♀ (female)"]
  J6 = female pin header, 2 pins [form="♀ (female)"]
  D2 = Rectifier Diode [part_number=1N4001 package="300 mil [THT]"]
  D3 = Rectifier Diode [part_number=1N4001 package="300 mil [THT]"]
  D4 = Rectifier Diode [part_number=1N4001 package="300 mil [THT]"]
  D5 = Rectifier Diode [part_number=1N4001 package="300 mil [THT]"]
  Arduino1 = Arduino
  D6 = Rectifier Diode [part_number=1N4001 package="300 mil [THT]"]
  D7 = Rectifier Diode [part_number=1N4001 package="300 mil [THT]"]
  D8 = Rectifier Diode [part_number=1N4001 package="300 mil [THT]"]
  D9 = Rectifier Diode [part_number=1N4001 package="300 mil [THT]"]

nets:
  N1: IC1.Enable_1, Arduino1.D11
  N2: IC1.In_1, Arduino1.D9
  N3: IC1.Out_1_(_Controlled_by_Enable_1_), J1.pin1, D2.anode, D3.cathode
  N4: IC1.0V, J5.pin1, J5.pin2, J6.pin1, J6.pin2, D3.anode, D4.anode, Arduino1.GND, D7.anode, D9.anode
  N5: IC1.Out_2_(_Controlled_by_Enable_1_), J1.pin2, D4.cathode, D5.anode
  N6: IC1.In_2, Arduino1.D2
  N7: IC1.+Vmotor, D2.cathode, D5.cathode, Arduino1.VIN, D6.cathode, D8.cathode
  N8: IC1.Enable_2, Arduino1.D3
  N9: IC1.In_3, Arduino1.D4
  N10: IC1.Out_3_(_Controlled_by_Enable_2_), J2.pin2, D6.anode, D7.cathode
  N11: IC1.Out_4_(_Controlled_by_Enable_2_), J2.pin1, D8.anode, D9.cathode
  N12: IC1.In_4, Arduino1.D8
  N13: IC1.+V, J3.pin1, J3.pin2, J4.pin1, J4.pin2, Arduino1.+5V
