# Fritzing sketch id2050_Tank_Setup_0 (saved by Fritzing 0.9.3b)
breadboards: 1

parts:
  Part1 = Arduino Mega 2560 (Rev3)
  U1 = BNC [package=bnc]
  pH_Circuit1 = pH Circuit
  U2 = 4ChannelRelay
  SD_card_module1 = SD_Card_Module.fzp
  U3 = G3VM-61E1 [package=g3vm-61e1]
  Tiny_RTC1 = tinyRTC
  U5 = 6675_efe
  S1 = Square Pushbutton
  R1 = Temperature Sensor (Thermistor) [thermistor_type=NTC package=THT]

nets:
  N1: Part1.A4, Tiny_RTC1.connector2
  N2: Part1.A5, Tiny_RTC1.connector1
  N3: Part1.D15/RX3, pH_Circuit1.TX
  N4: Part1.D14/TX3, pH_Circuit1.RX
  N5: Part1.D12_PWM, S1.leg0
  N6: Part1.D2_PWM, U2.connector10
  N7: Part1.D3_PWM, U2.connector2
  N8: Part1.D5_PWM, U5.connector6
  N9: Part1.D6_PWM, U5.connector5
  N10: Part1.D7_PWM, U5.connector4
  N11: Part1.D46, U3.P$1
  N12: Part1.D47, U3.P$3
  N13: Part1.D49, SD_card_module1.connector3
  N14: Part1.D50, SD_card_module1.connector6
  N15: Part1.D51, SD_card_module1.connector4
  N16: Part1.D52, SD_card_module1.connector5
  N17: U1.GND, pH_Circuit1.GND#5
  N18: U1.OUT, pH_Circuit1.PRB
  N19: pH_Circuit1.GND#0, U2.connector1, SD_card_module1.connector7, Tiny_RTC1.connector4, U5.connector3, S1.leg1
  N20: U2.connector0, SD_card_module1.connector2, Tiny_RTC1.connector3, U5.connector0
  N21: U5.connector1, R1.pin_1
  N22: U5.connector2, R1.pin_0
