# Fritzing sketch id2051_Helmet_Circuit_0 (saved by Fritzing 0.9.3b)
breadboards: 1

parts:
  12v_-_5v_1_5A = Voltage Regulator [package=to220-igo]
  12v_-_3v_2A = Voltage Regulator [package=to220-igo]
  12v_-_3v_2A_2 = Voltage Regulator [package=to220-igo]
  12v_-_7_5v_2A1 = Voltage Regulator [package=to220-igo]
  BAT1 = Battery Holders [package=battery-aa]
  BAT2 = Battery Holders [package=battery-aa]
  BAT3 = Battery Holders [package=battery-aa]
  BAT4 = Battery Holders [package=battery-aa]
  BAT5 = Battery Holders [package=battery-aa]
  BAT6 = Battery Holders [package=battery-aa]
  BAT7 = Battery Holders [package=battery-aa]
  BAT8 = Battery Holders [package=battery-aa]
  BAT9 = Battery Holders [package=battery-aa]
  BAT10 = Battery Holders [package=battery-aa]
  Charging_Connection = Power plug
  part = Power plug
  LED1 = LEDs [package=led10mm]
  Part1 = ws2812b [package="smd 2812b"]
  part_2 = ws2812b [package="smd 2812b"]
  Part3 = ws2812b [package="smd 2812b"]
  Part4 = ws2812b [package="smd 2812b"]
  part_3 = ws2812b [package="smd 2812b"]
  part_4 = ws2812b [package="smd 2812b"]
  LED2 = LEDs [package=led10mm]
  LED3 = LEDs [package=led10mm]
  LED4 = LEDs [package=led10mm]
  LED5 = LEDs [package=led10mm]
  LED6 = LEDs [package=led10mm]
  S1 = Pushbutton [package=THT]
  S2 = Pushbutton [package=THT]
  S3 = Pushbutton [package=THT]
  J1 = Camdenboss CTB0158-5 [part_number=CTB0158-5 package=THT]
  12v_-_3v_2A_3 = Voltage Regulator [package=to220-igo]
  J2 = Camdenboss CTB0158-5 [part_number=CTB0158-5 package=THT]
  M1 = DC Motor
  M2 = DC Motor
  M3 = DC Motor
  M4 = DC Motor
  M5 = DC Motor
  M6 = DC Motor
  S4 = SWITCH-MOMENTARY-2 [package=tactile_switch_smd-2]
  Power_plug1 = Power plug
  Digital_Panel_Meter_Voltage_DMS-20PC_by_Murata1 = Digital Panel Meter, Voltage, DMS-20PC
  SPKR1 = Loudspeaker
  U1 = MIC [package=mic-9.7mm]
  S5 = Pushbutton [package=THT]
  Digital_Panel_Meter_Voltage_DMS-20PC_by_Murata2 = Digital Panel Meter, Voltage, DMS-20PC

nets:
  N1: 12v_-_5v_1_5A.GND, J2.pin5, M1.pin_2, M2.pin_2, M3.pin_2, M4.pin_2, M5.pin_2, M6.pin_2
  N2: 12v_-_5v_1_5A.IN, J1.pin5
  N3: 12v_-_5v_1_5A.OUT, S4.1
  VSS: 12v_-_3v_2A.GND, part_3.VSS, part_4.VSS, J2.pin4
  N4: 12v_-_3v_2A.IN, J1.pin4
  N5: 12v_-_3v_2A.OUT, S1.leg0
  VSS_2: 12v_-_3v_2A_2.GND, part_2.VSS, Part3.VSS, J2.pin2
  N6: 12v_-_3v_2A_2.IN, J1.pin2
  N7: 12v_-_3v_2A_2.OUT, S3.leg0
  N8: 12v_-_7_5v_2A1.GND, J2.pin1, SPKR1.pin2, U1.2
  N9: 12v_-_7_5v_2A1.IN, J1.pin1
  N10: 12v_-_7_5v_2A1.OUT, S5.leg0
  N11: BAT1.-, BAT2.-, BAT3.-, BAT4.-, BAT5.-, BAT6.+, BAT7.+, BAT8.+, BAT9.+, BAT10.+
  GND: BAT1.+, BAT2.+, BAT3.+, BAT4.+, BAT5.+, Charging_Connection.GND, part.GND, Digital_Panel_Meter_Voltage_DMS-20PC_by_Murata1.3:_GND, Digital_Panel_Meter_Voltage_DMS-20PC_by_Murata2.3:_GND
  VCC: BAT6.-, BAT7.-, BAT8.-, BAT9.-, BAT10.-, Charging_Connection.VCC, part.VCC
  N12: LED1.C, Part1.DIN
  N13: LED1.A, Part1.DOUT
  VDD: Part1.VDD, Part4.VDD, S2.leg1
  VSS_3: Part1.VSS, Part4.VSS, 12v_-_3v_2A_3.GND, J2.pin3
  VDD_2: part_2.VDD, Part3.VDD, S3.leg1
  N14: part_2.DOUT, LED3.A
  N15: part_2.DIN, LED3.C
  N16: Part3.DOUT, LED4.A
  N17: Part3.DIN, LED4.C
  N18: Part4.DOUT, LED2.A
  N19: Part4.DIN, LED2.C
  VDD_3: part_3.VDD, part_4.VDD, S1.leg1
  N20: part_3.DOUT, LED5.A
  N21: part_3.DIN, LED5.C
  N22: part_4.DOUT, LED6.A
  N23: part_4.DIN, LED6.C
  N24: S2.leg0, 12v_-_3v_2A_3.OUT
  N25: J1.pin3, 12v_-_3v_2A_3.IN
  N26: J1.terminal_1, J1.terminal_2, J1.terminal_3, J1.terminal_4, J1.terminal_5, Power_plug1.VCC
  N27: J2.terminal_1, J2.terminal_2, J2.terminal_3, J2.terminal_4, J2.terminal_5, Power_plug1.GND
  N28: M1.pin_1, M2.pin_1, M3.pin_1, M4.pin_1, M5.pin_1, M6.pin_1, S4.2, Digital_Panel_Meter_Voltage_DMS-20PC_by_Murata1.1:_VCC, Digital_Panel_Meter_Voltage_DMS-20PC_by_Murata2.1:_VCC
  N29: SPKR1.pin1, U1.1, S5.leg1

notes:
  CREE XPG2
  2xRed
  4xWhite
  500mA @3v
  Micropuck LED Driver
  500mA @3v
  Voltage Regulators DC to DC
  35v - 10.5v to 7.5v 2A
  35v - 7v to 5v 1A
  25v - 3v to 3v 2A
  10 D Cell NiMH
  In series and Parallel:
  12V 100,000maH
  Est. 19hrs run time
  +VO
  -VO
  Digital Voltmeter
  2.5v-30v 5-20mA
  +/- leads
  Tie into motor switch
  Digital Thermometer
  7v-30v ???mA
  +/- leads and probe
  Tie into motor switch
  Voice Amplifier
  (Gutted and rewired)
  7.5v 150mA
  x6 Fans
  5v 70mA
