# Fritzing sketch id2053_lyskryss_oblig1_0 (saved by Fritzing 0.9.2b)
breadboards: 1

parts:
  part = Resistor [tolerance=±20% resistance=220 package=THT]
  knapp = Pushbutton [package="[THT]"]
  part_2 = Resistor [tolerance=±20% resistance=220 package=THT]
  part_3 = Resistor [tolerance=±20% resistance=220 package=THT]
  part_4 = Resistor [tolerance=±20% resistance=220 package=THT]
  part_5 = Resistor [tolerance=±20% resistance=220 package=THT]
  fotgjRod = LED - 5mm [color="Red (633nm)" package="5 mm [THT]"]
  bilGul = LED - 5mm [color="Yellow (592nm)" package="5 mm [THT]"]
  bilGronn = LED - 5mm [color="Green (555nm)" package="5 mm [THT]"]
  fotgjGronn = LED - 5mm [color="Green (555nm)" package="5 mm [THT]"]
  Lyskryss-krets = Arduino Uno (Rev3)
  part_6 = Resistor [tolerance=±0.5% resistance=10k package=THT]
  bilRod = LED - 5mm [color="Red (633nm)" package="5 mm [THT]"]

nets:
  N1: part.Pin_0, bilRod.anode
  N2: part.Pin_1, Lyskryss-krets.D13/SCK
  N3: knapp.Pin_1, knapp.Pin_2, part_6.Pin_0
  N4: knapp.Pin_3, knapp.Pin_4, Lyskryss-krets.5V
  N5: part_2.Pin_0, fotgjGronn.anode
  N6: part_2.Pin_1, Lyskryss-krets.D8
  N7: part_3.Pin_0, fotgjRod.anode
  N8: part_3.Pin_1, Lyskryss-krets.D9_PWM
  N9: part_4.Pin_0, bilGronn.anode
  N10: part_4.Pin_1, Lyskryss-krets.D10_PWM/SS
  N11: part_5.Pin_0, bilGul.anode
  N12: part_5.Pin_1, Lyskryss-krets.D12/MISO
  N13: fotgjRod.cathode, bilGul.cathode, bilGronn.cathode, fotgjGronn.cathode, Lyskryss-krets.GND, part_6.Pin_1, bilRod.cathode
