# Fritzing sketch id2054_LED_Circut_0 (saved by Fritzing 0.9.3b)
breadboards: 1

parts:
  Part1 = Arduino Uno (Rev3)
  V1 = DC Power [voltage=5]
  C1 = Electrolytic Capacitor [capacitance=4.7mF package="100 mil [THT, electrolytic]"]
  NEOPIXEL2 = Neopixel_Strip____Black__30_m
  NEOPIXEL3 = Neopixel_Strip____Black__30_m

nets:
  N1: Part1.GND, Part1.D6_PWM, NEOPIXEL2.connector2
  N2: V1.V+, C1.+, NEOPIXEL2.connector1
  N3: V1.V-, C1.-, NEOPIXEL2.connector3
  N4: NEOPIXEL2.connector4, NEOPIXEL3.connector3
  N5: NEOPIXEL2.connector5, NEOPIXEL3.connector2
  N6: NEOPIXEL2.connector6, NEOPIXEL3.connector1
