# Fritzing sketch id2055_infrared_transmitter_0 (saved by Fritzing 0.7.0b)
breadboards: 1

parts:
  U1 = 555 Timer [package="DIP8 [THT]"]
  R1 = Resistor [tolerance=±5% resistance=10k package=THT]
  R2 = Resistor [tolerance=±5% resistance=22k package=THT]
  R3 = Resistor [tolerance=±5% resistance=330 package=THT]
  LED1 = LED - 5mm [color="Infrared (850nm)" package="5 mm [THT]"]
  VCC1 = Battery block 9V
  C1 = Ceramic Capacitor [capacitance=1nF package="100 mil [THT, multilayer]"]

nets:
  N1: U1.Ground, LED1.cathode, VCC1.-, C1.0
  N2: U1.Trigger, U1.Threshold, R1.Pin_1, C1.1
  N3: U1.Output, R3.Pin_0
  N4: U1.Reset, U1.Vcc_Supply_Voltage, R2.Pin_0, VCC1.+
  N5: U1.Discharge, R1.Pin_0, R2.Pin_1
  N6: R3.Pin_1, LED1.anode

notes:
  IR LED
