# Fritzing sketch id2056_object_counter_0 (saved by Fritzing 0.7.0b)
breadboards: 3

parts:
  R1 = Resistor [tolerance=±5% resistance=15k package=THT]
  R2 = Resistor [tolerance=±5% resistance=1k package=THT]
  BC547 = NPN-Transistor [package="TO92 [THT]"]
  R3 = Resistor [tolerance=±5% resistance=330 package=THT]
  LED1 = LED - 5mm [color="Red (633nm)" package="5 mm [THT]"]
  S1 = Pushbutton [package="[THT]"]
  VCC1 = Battery block 9V
  C1 = Electrolytic Capacitor [capacitance=100µF package="200 mil [THT, electrolytic]"]  # not connected
  J2 = Infrared Proximity Sensor
  7805 = Voltage Regulator - 5V [package="TO220 [THT]"]
  R4 = Resistor [tolerance=±5% resistance=1k package=THT]
  BC557 = PNP-Transistor [package="TO92 [THT]"]
  R5 = Resistor [tolerance=±5% resistance=1k package=THT]
  LED2 = LED - 5mm [color="Red (633nm)" package="5 mm [THT]"]
  C3 = Ceramic Capacitor [capacitance=100nF package="100 mil [THT, multilayer]"]
  C4 = Ceramic Capacitor [capacitance=100nF package="100 mil [THT, multilayer]"]
  common_cathode1 = 7 Segment Display
  IC2 = IC, DIP package, 16 pins [chip_label=4026B spacing=300mil part_number=4026B]

nets:
  GND: R1.Pin_0, VCC1.-, J2.GND, 7805.GND, LED2.cathode, C3.0, C4.1, common_cathode1.common_cathode#3, IC2.pin2, IC2.pin8, IC2.pin15
  N1: R1.Pin_1, R2.Pin_0, S1.Pin_1, S1.Pin_2, R4.Pin_0, BC557.B
  N2: R2.Pin_1, BC547.B
  N3: BC547.E, LED1.cathode
  N4: R3.Pin_0, LED1.anode
  N5: R3.Pin_1, S1.Pin_3, S1.Pin_4, VCC1.+, 7805.input_voltage, C3.1, IC2.pin3, IC2.pin16
  N6: J2.Vout, R4.Pin_1
  N7: J2.Vcc, 7805.output_voltage, BC557.C, C4.0
  N8: BC557.E, R5.Pin_0
  N9: R5.Pin_1, LED2.anode
  N10: common_cathode1.Segment_A#1, IC2.pin7
  N11: common_cathode1.Segment_F, IC2.pin6
  N12: common_cathode1.Segment_E, IC2.pin11
  N13: common_cathode1.Segment_D, IC2.pin9
  N14: common_cathode1.Segment_C, IC2.pin13
  N15: common_cathode1.Segment_B, IC2.pin12
  N16: common_cathode1.Segment_A#10, IC2.pin10

notes:
  CLK
  Infrared sensor
