# Fritzing sketch id2057_IR_MUSIC_TRANSMITTER_AND_RECEIVER_0 (saved by Fritzing 0.7.0b)
breadboards: 3

parts:
  IC1 = IC, DIP package, 8 pins [chip_label=741 spacing=300mil]
  R1 = Trimmer Potentiometer [maximum_resistance=10kΩ package=THT]
  R2 = Resistor [tolerance=±5% resistance=100k package=THT]
  R3 = Resistor [tolerance=±5% resistance=10k package=THT]
  R4 = Resistor [tolerance=±5% resistance=15k package=THT]
  R5 = Resistor [tolerance=±5% resistance=10k package=THT]
  R6 = Resistor [tolerance=±5% resistance=15k package=THT]
  VCC1 = Battery block 9V
  LED2 = LED - 3mm [color="Infrared (940nm)" package="3 mm [THT]"]
  UM66 = NPN-Transistor [package="TO92 [THT]"]
  D2 = Zener Diode [breakdown_voltage=3.6V part_number=1N4732A package="300 mil [THT]"]
  C3 = Electrolytic Capacitor [capacitance=1µF package="0807 [SMD, electrolytic]"]
  R7 = Resistor [tolerance=±5% resistance=1k package=THT]
  S2 = Pushbutton [package="[THT]"]
  R8 = Resistor [tolerance=±5% resistance=4.7k package=THT]
  R9 = Resistor [tolerance=±5% resistance=22k package=THT]
  BC547 = NPN-Transistor [package="TO92 [THT]"]
  R10 = Resistor [tolerance=±5% resistance=100 package=THT]
  LED3 = LED - 5mm [color="Red (633nm)" package="5 mm [THT]"]
  BD140 = PNP-Transistor [package="TO92 [THT]"]
  R11 = Resistor [tolerance=±5% resistance=10 package=THT]
  C4 = Electrolytic Capacitor [capacitance=100µF package="200 mil [THT, electrolytic]"]
  LED4 = LED - 3mm [color="Infrared (850nm)" package="3 mm [THT]"]
  VCC2 = Battery block 9V
  IC2 = IC, DIP package, 8 pins [chip_label=LM386 spacing=300mil]
  C7 = Ceramic Capacitor [capacitance=100nF package="100 mil [THT, multilayer]"]
  R12 = Resistor [tolerance=±5% resistance=10 package=THT]
  C8 = Electrolytic Capacitor [capacitance=100µF voltage=20V package="200 mil [THT, electrolytic]"]
  SPKR2 = Loudspeaker
  C9 = Electrolytic Capacitor [capacitance=100µF voltage=20V package="200 mil [THT, electrolytic]"]
  C10 = Electrolytic Capacitor [capacitance=10µF voltage=20V package="100 mil [THT, electrolytic]"]
  C11 = Electrolytic Capacitor [capacitance=100µF voltage=20V package="200 mil [THT, electrolytic]"]
  R13 = Trimmer Potentiometer [maximum_resistance=10kΩ package=THT]
  C12 = Electrolytic Capacitor [capacitance=1000µF voltage=20V package="300 mil [THT, electrolytic]"]

nets:
  N1: IC1.pin2, R2.Pin_0, R3.Pin_1
  N2: IC1.pin3, R4.Pin_1, R6.Pin_0
  N3: IC1.pin4, R6.Pin_1, VCC1.-, LED2.anode, IC2.pin2, IC2.pin4, R12.Pin_1, SPKR2.pin1, C9.-, R13.leg1, C12.-
  N4: IC1.pin6, R1.leg2, R13.leg2
  N5: IC1.pin7, R4.Pin_0, R5.Pin_0, VCC1.+, IC2.pin6, C12.+
  N6: R1.wiper, R2.Pin_1
  N7: R3.Pin_0, R5.Pin_1, LED2.cathode
  N8: UM66.E, D2.anode, C3.-, R9.Pin_1, BC547.C, C4.-, LED4.cathode, VCC2.-
  N9: UM66.B, D2.cathode, C3.+, R7.Pin_0
  N10: UM66.C, R8.Pin_0
  N11: R7.Pin_1, S2.Pin_1, S2.Pin_2
  N12: S2.Pin_3, S2.Pin_4, LED3.anode, R11.Pin_0, C4.+, VCC2.+
  N13: R8.Pin_1, R9.Pin_0, BC547.B
  N14: BC547.E, R10.Pin_1
  N15: R10.Pin_0, LED3.cathode, BD140.B
  N16: BD140.E, R11.Pin_1
  N17: BD140.C, LED4.anode
  N18: IC2.pin1, C10.+
  N19: IC2.pin3, C11.-
  N20: IC2.pin5, C7.0, C8.+
  N21: IC2.pin7, C9.+
  N22: IC2.pin8, C10.-
  N23: C7.1, R12.Pin_0
  N24: C11.+, R13.wiper

notes:
  Fritzing does not have UM66, so we use NPN transistor to represent UM66
  IR LED
  Audio In
  photodiode
