# Fritzing sketch id2058_remote_tester_and_PWM_0 (saved by Fritzing 0.7.0b)
breadboards: 1

parts:
  J1 = Infrared Proximity Sensor
  Arduino1 = Arduino
  LED1 = LED - 3mm [color="Red (633nm)" package="3 mm [THT]"]

nets:
  N1: J1.Vout, Arduino1.D2
  GND: J1.GND, Arduino1.GND, LED1.cathode
  VCC: J1.Vcc, Arduino1.+5V
  N2: Arduino1.D9, LED1.anode
