# Fritzing sketch id205_Schematic_0 (saved by Fritzing 0.9.1b)
breadboards: 1

parts:
  R1 = Resistor [tolerance=±5% resistance=100k package=THT]
  R2 = Resistor [tolerance=±5% resistance=330 package=THT]
  Q1 = NPN-Transistor [part_number=2N3904 package="TO92 [THT]"]
  LED1 = LED - 5mm [color="Blue (470nm)" package="5 mm [THT]"]
  LDR = Photocell (LDR) [package=THT]

nets:
  N1: R1.Pin_0, Q1.B, LDR.pin_0
  5V: R1.Pin_1, R2.Pin_1
  N2: R2.Pin_0, LED1.anode
  GND: Q1.E, LDR.pin_1
  N3: Q1.C, LED1.cathode

notes:
  5V Supply
