# Fritzing sketch id2061_input_buffer_0 (saved by Fritzing 0.7.7b)
breadboards: 2

parts:
  Arduino1 = Arduino
  S1 = Toggle Switch [package=THT]
  S2 = Toggle Switch [package=THT]
  S3 = Toggle Switch [package=THT]
  S4 = Toggle Switch [package=THT]
  S5 = Toggle Switch [package=THT]
  S6 = Toggle Switch [package=THT]
  S7 = Toggle Switch [package=THT]
  S8 = Toggle Switch [package=THT]
  R1 = Resistor [tolerance=±5% resistance=1k package=THT]
  R2 = Resistor [tolerance=±5% resistance=1k package=THT]
  R3 = Resistor [tolerance=±5% resistance=1k package=THT]
  R4 = Resistor [tolerance=±5% resistance=1k package=THT]
  R5 = Resistor [tolerance=±5% resistance=1k package=THT]
  R6 = Resistor [tolerance=±5% resistance=1k package=THT]
  R7 = Resistor [tolerance=±5% resistance=1k package=THT]
  R8 = Resistor [tolerance=±5% resistance=1k package=THT]
  LED1 = LED - 5mm [color="Red (633nm)" package="5 mm [THT]"]
  LED2 = LED - 5mm [color="Red (633nm)" package="5 mm [THT]"]
  LED3 = LED - 5mm [color="Red (633nm)" package="5 mm [THT]"]
  LED4 = LED - 5mm [color="Red (633nm)" package="5 mm [THT]"]
  LED5 = LED - 5mm [color="Red (633nm)" package="5 mm [THT]"]
  LED6 = LED - 5mm [color="Red (633nm)" package="5 mm [THT]"]
  LED7 = LED - 5mm [color="Red (633nm)" package="5 mm [THT]"]
  LED8 = LED - 5mm [color="Red (633nm)" package="5 mm [THT]"]

nets:
  N1: Arduino1.GND, R1.Pin_1, R3.Pin_1, R4.Pin_1, R5.Pin_1, R6.Pin_1, R7.Pin_1, LED1.cathode, LED2.cathode, LED3.cathode, LED4.cathode, LED5.cathode, LED6.cathode, LED7.cathode, LED8.cathode
  N2: Arduino1.D13, LED3.anode
  N3: Arduino1.D12, LED4.anode
  N4: Arduino1.D11, LED5.anode
  N5: Arduino1.D10, LED6.anode
  N6: Arduino1.D9, LED7.anode
  N7: Arduino1.D8, LED8.anode
  N8: Arduino1.D7, S6.COM, S6.L2, R3.Pin_0
  N9: Arduino1.D6, S5.COM, S5.L2, R4.Pin_0
  N10: Arduino1.D5, S4.COM, S4.L2, R5.Pin_0
  N11: Arduino1.D4, S3.COM, S3.L2, R6.Pin_0
  N12: Arduino1.D3, S2.COM, S2.L2, R7.Pin_0
  N13: Arduino1.D2, S1.COM, S1.L2, R8.Pin_0
  N14: Arduino1.+5V, S1.L1, S2.L1, S3.L1, S4.L1, S5.L1, S6.L1, S7.L1, S8.L1
  N15: Arduino1.A0, LED2.anode
  N16: Arduino1.A1, LED1.anode
  N17: Arduino1.A2, S7.COM, S7.L2, R2.Pin_0
  N18: Arduino1.A3, S8.COM, S8.L2, R1.Pin_0
