# Fritzing sketch id2063_inseguitore_solare_0 (saved by Fritzing 0.8.5b)
breadboards: 1

parts:
  Part1 = Arduino Uno (Rev3)
  J1 = Basic Servo
  J2 = Basic Servo
  R1 = Photocell (LDR) [package=THT]
  R2 = Photocell (LDR) [package=THT]
  R3 = Photocell (LDR) [package=THT]
  R4 = Resistor [tolerance=±5% resistance=220 package=THT]
  R5 = Resistor [tolerance=±5% resistance=220 package=THT]
  R6 = Photocell (LDR) [package=THT]

nets:
  N1: Part1.A0, R2.pin_1, R3.pin_0
  N2: Part1.A1, R2.pin_0, R4.Pin_1
  N3: Part1.A2, R1.pin_1, R6.pin_0
  N4: Part1.A3, R1.pin_0, R5.Pin_1
  N5: Part1.D9_PWM, J1.pulse
  N6: Part1.D10_PWM/SS, J2.pulse
  VCC: Part1.5V, J1.vcc, J2.vcc, R4.Pin_0, R5.Pin_0
  GND: Part1.GND, J1.gnd, J2.gnd, R3.pin_1, R6.pin_1

notes:
  Servo pan
  Servo tilt
  FR 1 - 2 -3 - 4
  R1 = R2 = 220 OHM
