# Fritzing sketch id2064_shield_amplificador_de_termocupla_arduino_1_0 (saved by Fritzing 0.8.5b)
circuit board: 6.88566cm x 5.36311cm
breadboards: 1

parts:
  LM358 = LM 358 Dual Op-Amp [package="DIP8 [THT]"]
  R1- = Resistor [tolerance=±5% resistance=100k package=THT]
  R1 = Resistor [tolerance=±5% resistance=100k package=THT]
  R2 = Resistor [tolerance=±5% resistance=100k package=THT]
  R2- = Resistor [tolerance=±5% resistance=100k package=THT]
  Thermocouple_amplifier_shield_for_arduino = Arduino Uno (Rev3)
  R3 = Resistor [tolerance=±5% resistance=100k package=THT]
  R3- = Resistor [tolerance=±5% resistance=100k package=THT]
  LM358_2 = LM 358 Dual Op-Amp [package="DIP8 [THT]"]
  Termocupla = Screw terminal - 2 pins [package=THT]
  TEMP-REF = LM35 Temperature Sensor [package="TO92 [THT]"]
  R5 = Resistor [tolerance=±5% resistance=1k package=THT]
  R4 = Resistor [tolerance=±5% resistance=1k package=THT]
  C1 = Ceramic Capacitor [capacitance=1nF package="100 mil [THT, multilayer]"]
  C2 = Ceramic Capacitor [capacitance=1µF package="100 mil [THT, multilayer]"]
  C3 = Ceramic Capacitor [capacitance=1nF package="100 mil [THT, multilayer]"]
  R6 = Resistor [tolerance=±5% resistance=1M package=THT]
  Rg = Resistor [tolerance=±5% resistance=2.2k package=THT]
  SSR = Screw terminal - 2 pins [package=THT]

nets:
  N1: LM358.connector0, R1.Pin_1, R2.Pin_0
  N2: LM358.connector1, R1.Pin_0, Rg.Pin_0
  N3: LM358.connector2, R5.Pin_1, C1.1, C2.1
  GND: LM358.connector3, Thermocouple_amplifier_shield_for_arduino.GND, R3-.Pin_0, LM358_2.connector3, TEMP-REF.GND, C1.0, C3.0, R6.Pin_1, SSR.pin2
  N4: LM358.connector4, R4.Pin_1, C2.0, C3.1
  N5: LM358.connector5, R1-.Pin_1, Rg.Pin_1
  N6: LM358.connector6, R1-.Pin_0, R2-.Pin_0
  N7: LM358.connector7, Thermocouple_amplifier_shield_for_arduino.VIN, LM358_2.connector7
  N8: R2.Pin_1, R3.Pin_0, LM358_2.connector1
  N9: R2-.Pin_1, R3-.Pin_1, LM358_2.connector2
  N10: Thermocouple_amplifier_shield_for_arduino.A0, TEMP-REF.Vout
  N11: Thermocouple_amplifier_shield_for_arduino.A1, R3.Pin_1, LM358_2.connector0
  N12: Thermocouple_amplifier_shield_for_arduino.D13/SCK, SSR.pin1
  N13: Thermocouple_amplifier_shield_for_arduino.5V, TEMP-REF.+Vs
  N14: Termocupla.pin1, R4.Pin_0
  N15: Termocupla.pin2, R5.Pin_0, R6.Pin_0

notes:
  This is usesless when you can buy a ready to use and cheap instrumental ampliffier, in my case I need a thermocouple ampliffier.
  When you cannot buy it because is unavailable, this could be a solution.
  This has not could junction compensation, it can be added via software using nist.org equations and a cheap temperature sensor near the screw connector.
  +
  -
  Miguelangel Leon 2013/12/26
  Universidad Central de Venezuela
  Rev0.2
