# Fritzing sketch id2065_Thermocouple_amplifier_shiled_for_arduino_0 (saved by Fritzing 0.8.5b)
circuit board: 6.88566cm x 5.36311cm
breadboards: 1

parts:
  U1 = LM 358 Dual Op-Amp [package="DIP8 [THT]"]
  Rg = Resistor [tolerance=±5% resistance=2.2k package=THT]
  R1- = Resistor [tolerance=±5% resistance=100k package=THT]
  R1 = Resistor [tolerance=±5% resistance=100k package=THT]
  R2 = Resistor [tolerance=±5% resistance=100k package=THT]
  R2- = Resistor [tolerance=±5% resistance=100k package=THT]
  CCPP_Thermocouple_In_Amp_for_arduino_Rev0_1 = Arduino Uno (Rev3)
  R3 = Resistor [tolerance=±5% resistance=100k package=THT]
  R3- = Resistor [tolerance=±5% resistance=100k package=THT]
  U2 = LM 358 Dual Op-Amp [package="DIP8 [THT]"]
  Termocupla = Screw terminal - 2 pins [package=THT]
  TEMP-REF = LM35 Temperature Sensor [package="TO92 [THT]"]
  R5 = Resistor [tolerance=±5% resistance=1k package=THT]
  R4 = Resistor [tolerance=±5% resistance=1k package=THT]
  C1 = Ceramic Capacitor [capacitance=1nF package="100 mil [THT, multilayer]"]
  C2 = Ceramic Capacitor [capacitance=1µF package="100 mil [THT, multilayer]"]
  C3 = Ceramic Capacitor [capacitance=1nF package="100 mil [THT, multilayer]"]
  R6 = Resistor [tolerance=±5% resistance=1M package=THT]

nets:
  N1: U1.connector0, R1.Pin_1, R2.Pin_0
  N2: U1.connector1, Rg.Pin_0, R1.Pin_0
  N3: U1.connector2, R5.Pin_1, C1.1, C2.1
  GND: U1.connector3, CCPP_Thermocouple_In_Amp_for_arduino_Rev0_1.GND, R3-.Pin_1, U2.connector3, TEMP-REF.GND, C1.0, C3.0, R6.Pin_1
  N4: U1.connector4, R4.Pin_1, C2.0, C3.1
  N5: U1.connector5, Rg.Pin_1, R1-.Pin_1
  N6: U1.connector6, R1-.Pin_0, R2-.Pin_0
  N7: U1.connector7, CCPP_Thermocouple_In_Amp_for_arduino_Rev0_1.VIN, U2.connector7
  N8: R2.Pin_1, R3.Pin_0, U2.connector1
  N9: R2-.Pin_1, R3-.Pin_0, U2.connector2
  N10: CCPP_Thermocouple_In_Amp_for_arduino_Rev0_1.A0, TEMP-REF.Vout
  N11: CCPP_Thermocouple_In_Amp_for_arduino_Rev0_1.A1, R3.Pin_1, U2.connector0
  N12: CCPP_Thermocouple_In_Amp_for_arduino_Rev0_1.5V, TEMP-REF.+Vs
  N13: Termocupla.pin1, R4.Pin_0
  N14: Termocupla.pin2, R5.Pin_0, R6.Pin_0

notes:
  This is usesless when you can buy a ready to use and cheap instrumental ampliffier, in my case I need a thermocouple ampliffier.
  When you cannot buy it because is unavailable, this could be a solution.
  This has not could junction compensation, it can be added via software using nist.org equations and a cheap temperature sensor near the screw connector.
  +
  UCV Miguelangel Leon
  12/23/2013 Creative Commons
  -
