# Fritzing sketch id2067_intelligent_battery_charger_0 (saved by Fritzing 0.7.4b)
stripboards: 1

parts:
  Power_plug4 = Power plug
  U1 = atmega328 [package=dip]
  J19 = male pin header, 5 pins [form="♂ (male)"]
  U7 = Voltage Regulator - Variable [package="TO220 [THT]"]
  R6 = Resistor [tolerance=±5% resistance=1 part_number="1r0 5W" package=THT]
  R7 = Resistor [tolerance=±5% resistance=1k package=THT]
  R8 = Resistor [tolerance=±5% resistance=3.3k package=THT]
  R9 = Resistor [tolerance=±5% resistance=1k package=THT]
  D5 = Rectifier Diode [part_number=1N5404 package="300 mil [THT]"]
  R10 = Resistor [tolerance=±5% resistance=330k package=THT]
  R11 = Resistor [tolerance=±5% resistance=100k package=THT]
  VCC1 = 4 x AAA Battery Mount
  R13 = Resistor [tolerance=±5% resistance=220 package=THT]
  LED1 = LED - 5mm [color="Red (633nm)" package="5 mm [THT]"]
  J20 = male pin header, 5 pins [form="♂ (male)"]
  J21 = Screw terminal - 2 pins [package=THT]
  D4 = Rectifier Diode [part_number=1N4001 package="300 mil [THT]"]
  Q2 = bc548b_NPN_Transistor [part_number=bc548b]
  C16 = Electrolytic Capacitor [capacitance=47µF package="200 mil [THT, electrolytic]"]
  C17 = Electrolytic Capacitor [capacitance=1µF package="200 mil [THT, electrolytic]"]
  U6 = Voltage Regulator - 5V [package="TO220 [THT]"]
  R5 = Resistor [tolerance=±5% resistance=1k package=THT]
  XTAL4 = Crystal [frequency="16 Mhz" package=THT]
  C14 = Ceramic Capacitor [capacitance=22pF package="100 mil [THT, multilayer]"]
  C15 = Ceramic Capacitor [capacitance=22pF package="100 mil [THT, multilayer]"]

nets:
  GND: Power_plug4.GND, U1.GND, R11.Pin_1, VCC1.-, LED1.cathode, J20.pin2, J21.pin1, Q2.connector3, C16.-, C17.-, U6.GND, C14.0, C15.1
  N1: Power_plug4.VCC, D4.anode
  N2: U1.RESET, J19.pin3, R5.Pin_0
  N3: U1.VCC, U1.AVCC, U1.AREF, R9.Pin_0, C17.+, U6.output_voltage, R5.Pin_1
  N4: U1.XLAT1, XTAL4.pin_0, C14.1
  N5: U1.XLAT2, XTAL4.pin_1, C15.0
  N6: U1.D6_(PWM), R8.Pin_0, R9.Pin_1
  N7: U1.D9_(PWM), R13.Pin_0
  N8: U1.D11_(PWM), J19.pin1
  N9: U1.D12, J19.pin5
  N10: U1.D13, J19.pin4
  N11: U1.A5, R10.Pin_1, R11.Pin_0
  N12: U7.ADJ, R7.Pin_0, Q2.connector4
  N13: U7.OUT, R6.Pin_0
  N14: U7.IN, D4.cathode, C16.+, U6.input_voltage
  N15: R6.Pin_1, R7.Pin_1, D5.anode
  N16: R8.Pin_1, Q2.connector1
  N17: D5.cathode, R10.Pin_0, VCC1.+, J21.pin2
  N18: R13.Pin_1, LED1.anode

notes:
  ICSP header
  1 2
  MOSI VTG
  NC GND
  RST GND
  SCK GND
  MISO GND
  ICSP header
  MOSI
  NC
  RST
  SCK
  MISO
  Voltage sensor.
  R10 + R11 acts as a voltage divider.
  Calculate values based on max voltage supplied.
