# Fritzing sketch id2068_Kurelek_0 (saved by Fritzing 0.9.3b)
breadboards: 1

parts:
  Raspberry_Pi_1 = Raspberry Pi 3 [part_number=RPI-3-V1.2]
  Part1 = US-100 Ultrasonic Rangefinder
  TTP223B8 = richardbruneau00000
  TTP223B9 = richardbruneau00000
  TTP223B10 = richardbruneau00000
  TTP223B11 = richardbruneau00000
  TTP223B12 = richardbruneau00000
  TTP223B13 = richardbruneau00000
  TTP223B14 = richardbruneau00000
  TTP223B15 = richardbruneau00000
  TTP223B16 = richardbruneau00000
  TTP223B17 = richardbruneau00000

nets:
  3V3: Raspberry_Pi_1.3v3, Raspberry_Pi_1.3V3, Raspberry_Pi_1.5V, Part1.connector8, TTP223B8.connector9, TTP223B9.connector9, TTP223B10.connector9, TTP223B11.connector9, TTP223B12.connector9, TTP223B13.connector8, TTP223B13.connector9, TTP223B14.connector9, TTP223B15.connector9, TTP223B16.connector9, TTP223B17.connector9
  N1: Raspberry_Pi_1.GIPO4, TTP223B17.connector10
  N2: Raspberry_Pi_1.GIPO6, TTP223B12.connector10
  N3: Raspberry_Pi_1.GIPO13, Raspberry_Pi_1.GND, Part1.connector12, TTP223B8.connector8, TTP223B9.connector8, TTP223B10.connector8, TTP223B11.connector8, TTP223B11.connector10, TTP223B12.connector8, TTP223B13.connector10, TTP223B14.connector8, TTP223B15.connector8, TTP223B16.connector8, TTP223B17.connector8
  N4: Raspberry_Pi_1.GIPO19, TTP223B14.connector10
  N5: Raspberry_Pi_1.GIPO26, TTP223B15.connector10
  N6: Raspberry_Pi_1.GIPO21, TTP223B8.connector10
  N7: Raspberry_Pi_1.GIPO20, TTP223B9.connector10
  N8: Raspberry_Pi_1.GIPO16, TTP223B10.connector10
  N9: Raspberry_Pi_1.GIPO12, TTP223B16.connector10
  N10: Raspberry_Pi_1.GIPO15, Part1.connector9
  N11: Raspberry_Pi_1.GIPO14, Part1.connector10
