# Fritzing sketch id2069_8_x_8_leds_matrix_with_2_x_74hc595_Ktbp6jFUAH (saved by Fritzing 0.9.3b)
breadboards: 2

parts:
  LED41 = LED - 5mm [color="Red (633nm)" package="5 mm [THT]"]
  LED42 = LED - 5mm [color="Red (633nm)" package="5 mm [THT]"]
  LED43 = LED - 5mm [color="Red (633nm)" package="5 mm [THT]"]
  LED44 = LED - 5mm [color="Red (633nm)" package="5 mm [THT]"]
  LED45 = LED - 5mm [color="Red (633nm)" package="5 mm [THT]"]
  LED46 = LED - 5mm [color="Red (633nm)" package="5 mm [THT]"]
  LED47 = LED - 5mm [color="Red (633nm)" package="5 mm [THT]"]
  LED48 = LED - 5mm [color="Red (633nm)" package="5 mm [THT]"]
  LED49 = LED - 5mm [color="Red (633nm)" package="5 mm [THT]"]
  LED50 = LED - 5mm [color="Red (633nm)" package="5 mm [THT]"]
  LED51 = LED - 5mm [color="Red (633nm)" package="5 mm [THT]"]
  LED52 = LED - 5mm [color="Red (633nm)" package="5 mm [THT]"]
  LED53 = LED - 5mm [color="Red (633nm)" package="5 mm [THT]"]
  LED54 = LED - 5mm [color="Red (633nm)" package="5 mm [THT]"]
  LED55 = LED - 5mm [color="Red (633nm)" package="5 mm [THT]"]
  LED56 = LED - 5mm [color="Red (633nm)" package="5 mm [THT]"]
  LED57 = LED - 5mm [color="Red (633nm)" package="5 mm [THT]"]
  LED58 = LED - 5mm [color="Red (633nm)" package="5 mm [THT]"]
  LED59 = LED - 5mm [color="Red (633nm)" package="5 mm [THT]"]
  LED60 = LED - 5mm [color="Red (633nm)" package="5 mm [THT]"]
  LED61 = LED - 5mm [color="Orange (620nm)" package="5 mm [THT]"]
  LED62 = LED - 5mm [color="Red (633nm)" package="5 mm [THT]"]
  LED63 = LED - 5mm [color="Red (633nm)" package="5 mm [THT]"]
  LED64 = LED - 5mm [color="Red (633nm)" package="5 mm [THT]"]
  LED65 = LED - 5mm [color="Red (633nm)" package="5 mm [THT]"]
  LED66 = LED - 5mm [color="Red (633nm)" package="5 mm [THT]"]
  LED67 = LED - 5mm [color="Red (633nm)" package="5 mm [THT]"]
  LED68 = LED - 5mm [color="Red (633nm)" package="5 mm [THT]"]
  LED69 = LED - 5mm [color="Red (633nm)" package="5 mm [THT]"]
  LED70 = LED - 5mm [color="Red (633nm)" package="5 mm [THT]"]
  LED71 = LED - 5mm [color="Red (633nm)" package="5 mm [THT]"]
  LED72 = LED - 5mm [color="Red (633nm)" package="5 mm [THT]"]
  LED73 = LED - 5mm [color="Red (633nm)" package="5 mm [THT]"]
  LED74 = LED - 5mm [color="Red (633nm)" package="5 mm [THT]"]
  LED75 = LED - 5mm [color="Red (633nm)" package="5 mm [THT]"]
  LED76 = LED - 5mm [color="Red (633nm)" package="5 mm [THT]"]
  LED77 = LED - 5mm [color="Red (633nm)" package="5 mm [THT]"]
  LED78 = LED - 5mm [color="Red (633nm)" package="5 mm [THT]"]
  LED79 = LED - 5mm [color="Red (633nm)" package="5 mm [THT]"]
  LED80 = LED - 5mm [color="Red (633nm)" package="5 mm [THT]"]
  LED81 = LED - 5mm [color="Red (633nm)" package="5 mm [THT]"]
  LED82 = LED - 5mm [color="Red (633nm)" package="5 mm [THT]"]
  LED83 = LED - 5mm [color="Red (633nm)" package="5 mm [THT]"]
  LED84 = LED - 5mm [color="Red (633nm)" package="5 mm [THT]"]
  LED85 = LED - 5mm [color="Red (633nm)" package="5 mm [THT]"]
  LED86 = LED - 5mm [color="Red (633nm)" package="5 mm [THT]"]
  LED87 = LED - 5mm [color="Red (633nm)" package="5 mm [THT]"]
  LED88 = LED - 5mm [color="Red (633nm)" package="5 mm [THT]"]
  LED89 = LED - 5mm [color="Red (633nm)" package="5 mm [THT]"]
  LED90 = LED - 5mm [color="Red (633nm)" package="5 mm [THT]"]
  LED91 = LED - 5mm [color="Red (633nm)" package="5 mm [THT]"]
  LED92 = LED - 5mm [color="Red (633nm)" package="5 mm [THT]"]
  LED93 = LED - 5mm [color="Red (633nm)" package="5 mm [THT]"]
  LED94 = LED - 5mm [color="Red (633nm)" package="5 mm [THT]"]
  LED95 = LED - 5mm [color="Red (633nm)" package="5 mm [THT]"]
  LED96 = LED - 5mm [color="Red (633nm)" package="5 mm [THT]"]
  LED97 = LED - 5mm [color="Red (633nm)" package="5 mm [THT]"]
  LED98 = LED - 5mm [color="Red (633nm)" package="5 mm [THT]"]
  LED99 = LED - 5mm [color="Red (633nm)" package="5 mm [THT]"]
  LED100 = LED - 5mm [color="Red (633nm)" package="5 mm [THT]"]
  LED101 = LED - 5mm [color="Red (633nm)" package="5 mm [THT]"]
  LED102 = LED - 5mm [color="Red (633nm)" package="5 mm [THT]"]
  LED103 = LED - 5mm [color="Red (633nm)" package="5 mm [THT]"]
  LED104 = LED - 5mm [color="Red (633nm)" package="5 mm [THT]"]
  U1 = 74HC595 [package="DIP16 [THT]"]
  U2 = 74HC595 [package="DIP16 [THT]"]
  R1 = Resistor [tolerance=±5% resistance=220 package=THT]
  R2 = Resistor [tolerance=±5% resistance=220 package=THT]
  R3 = Resistor [tolerance=±5% resistance=220 package=THT]
  R4 = Resistor [tolerance=±5% resistance=220 package=THT]
  R5 = Resistor [tolerance=±5% resistance=220 package=THT]
  R6 = Resistor [tolerance=±5% resistance=220 package=THT]
  R7 = Resistor [tolerance=±5% resistance=220 package=THT]
  Part1 = Arduino Mega 2560 (Rev3)
  S1 = Pushbutton [package="[THT]"]
  S2 = Pushbutton [package="[THT]"]
  S3 = Pushbutton [package="[THT]"]
  S4 = Pushbutton [package="[THT]"]
  LCD1 = LCD screen
  R8 = Trimmer Potentiometer [maximum_resistance=10kΩ package=THT]
  R9 = Resistor [tolerance=±5% resistance=220 package=THT]

nets:
  N1: LED41.anode, LED42.anode, LED43.anode, LED44.anode, LED45.anode, LED46.anode, LED47.anode, LED48.anode, R9.Pin_0
  N2: LED42.cathode, LED55.cathode, LED62.cathode, LED70.cathode, LED78.cathode, LED86.cathode, LED94.cathode, LED102.cathode
  N3: LED44.cathode, LED52.cathode, LED59.cathode, LED67.cathode, LED75.cathode, LED83.cathode, LED91.cathode, LED99.cathode
  N4: LED46.cathode, LED54.cathode, LED58.cathode, LED66.cathode, LED74.cathode, LED82.cathode, LED90.cathode, LED98.cathode
  N5: LED47.cathode, LED49.cathode, LED63.cathode, LED71.cathode, LED79.cathode, LED87.cathode, LED95.cathode, LED103.cathode
  N6: LED48.cathode, LED51.cathode, LED61.cathode, LED69.cathode, LED77.cathode, LED85.cathode, LED93.cathode, LED101.cathode
  N7: LED49.anode, LED50.anode, LED51.anode, LED52.anode, LED53.anode, LED54.anode, LED55.anode, LED56.anode, R1.Pin_0
  N8: LED57.anode, LED58.anode, LED59.anode, LED60.anode, LED61.anode, LED62.anode, LED63.anode, LED64.anode, R2.Pin_0
  N9: LED64.cathode, LED72.cathode, LED80.cathode, LED88.cathode, LED96.cathode, LED104.cathode
  N10: LED65.anode, LED66.anode, LED67.anode, LED68.anode, LED69.anode, LED70.anode, LED71.anode, LED72.anode, R3.Pin_0
  N11: LED73.anode, LED74.anode, LED75.anode, LED76.anode, LED77.anode, LED78.anode, LED79.anode, LED80.anode, R4.Pin_0
  N12: LED81.anode, LED82.anode, LED83.anode, LED84.anode, LED85.anode, LED86.anode, LED87.anode, LED88.anode, R5.Pin_0
  N13: LED89.anode, LED90.anode, LED91.anode, LED92.anode, LED93.anode, LED94.anode, LED95.anode, LED96.anode, R6.Pin_0
  N14: LED97.anode, LED98.anode, LED99.anode, LED100.anode, LED101.anode, LED102.anode, LED103.anode, LED104.anode, R7.Pin_0
  N15: U1.Q1, R1.Pin_1
  N16: U1.Q2, R2.Pin_1
  N17: U1.Q3, R3.Pin_1
  N18: U1.Q4, R4.Pin_1
  N19: U1.Q5, R5.Pin_1
  N20: U1.Q6, R6.Pin_1
  N21: U1.Q7, R7.Pin_1
  GND: U1.GND, U1.OE, U2.GND, U2.OE, Part1.GND, S1.Pin_1, S1.Pin_2, S2.Pin_1, S2.Pin_2, S3.Pin_1, S3.Pin_2, S4.Pin_1, S4.Pin_2, LCD1.VSS, LCD1.R/W, LCD1.LED-, R8.leg1
  VCC: U1.MR, U1.VCC, U2.MR, U2.VCC, Part1.5V, LCD1.VDD, LCD1.LED+, R8.leg2
  N22: U1.SH_CP, Part1.D7_PWM
  N23: U1.ST_CP, Part1.D6_PWM
  N24: U1.DS, Part1.D5_PWM
  N25: U1.Q0, R9.Pin_1
  N26: U2.SH_CP, Part1.D2_PWM
  N27: U2.ST_CP, Part1.D3_PWM
  N28: U2.DS, Part1.D4_PWM
  N29: Part1.A0, S3.Pin_3, S3.Pin_4
  N30: Part1.A1, S2.Pin_3, S2.Pin_4
  N31: Part1.A2, S1.Pin_3, S1.Pin_4
  N32: Part1.A3, S4.Pin_3, S4.Pin_4
  N33: Part1.D13_PWM, LCD1.DB7
  N34: Part1.D12_PWM, LCD1.DB6
  N35: Part1.D11_PWM, LCD1.DB5
  N36: Part1.D10_PWM, LCD1.DB4
  N37: Part1.D9_PWM, LCD1.E
  N38: Part1.D8_PWM, LCD1.RS
  N39: LCD1.V0, R8.wiper

notes:
  GND's Shifter
  All outputs active on LOW
  - 1, -2 ... -8
  PLUS's Shifter
  All outputs active on HIGH
  +1, +2, ... +8
  Page switch
  Next/Plus
  Previous/Minus
  ON/OFF
  Brightness Control
