# Fritzing sketch id2069_duedc_0 (saved by Fritzing 0.9.0b)
breadboards: 1

parts:
  Part1 = Arduino Due (Rev2b)
  IC1 = L293D [package=THT]
  M1 = DC Motor
  M2 = DC Motor

nets:
  N1: Part1.5V, IC1.Enable_1, IC1.+Vmotor, IC1.Enable_2, IC1.+V
  N2: Part1.GND, IC1.0V
  N3: IC1.Out_1_(_Controlled_by_Enable_1_), IC1.Out_2_(_Controlled_by_Enable_1_), M2.pin_1, M2.pin_2
  N4: IC1.In_3, M1.pin_2
  N5: IC1.Out_4_(_Controlled_by_Enable_2_), M1.pin_1

notes:
  int motor=46;
  int motor1=48;
  int motor2=50;
  int motor3=52;
  void setup()
  {
  pinMode(motor,OUTPUT);
  pinMode(motor1,OUTPUT);
  pinMode(motor2,OUTPUT);
  pinMode(motor3,OUTPUT);
  }
  void loop()
  {
  digitalWrite(motor,HIGH);
  digitalWrite(motor1,LOW);
  delay(1000);
  digitalWrite(motor,LOW);
  digitalWrite(motor1,HIGH);
  delay(1000);
  digitalWrite(motor2,HIGH);
  digitalWrite(motor3,LOW);
  delay(1000);
  digitalWrite(motor2,LOW);
  digitalWrite(motor3,HIGH);
  delay(1000);
  }
