# Fritzing sketch id206_lav55_0 (saved by Fritzing 0.9.3b)
circuit board: 6.14812cm x 4.57938cm
breadboards: 1

parts:
  Espessif_Serial_Wifi_Modul_1 = ESP8266_Wifi_Modul [part_number=ESP8266]
  Componente2 = Arduino Pro Mini v13
  Photoresistor = PHOTOCELL [package=photocell]
  R3 = Resistor [tolerance=±5% resistance=220 package="0603 [SMD]"]
  R4 = Resistor [tolerance=±5% resistance=220 package="0603 [SMD]"]
  3xAAA = Battery Holders [package=battery-aa]
  NTC_10K = Temperature Sensor (Thermistor) [thermistor_type=NTC package=THT]

nets:
  GND: Espessif_Serial_Wifi_Modul_1.connector0, Componente2.GND, Photoresistor.P$2, 3xAAA.-, NTC_10K.pin_0
  N1: Espessif_Serial_Wifi_Modul_1.connector1, Componente2.D9_PWM
  N2: Espessif_Serial_Wifi_Modul_1.connector2, Componente2.D10_PWM/SS
  N3: Espessif_Serial_Wifi_Modul_1.connector3, Componente2.VCC, R3.Pin_0, R4.Pin_0, 3xAAA.+
  N4: Espessif_Serial_Wifi_Modul_1.connector7, Componente2.D11_PWM/MOSI
  N5: Componente2.A1, R3.Pin_1, NTC_10K.pin_1
  N6: Componente2.A0, Photoresistor.P$1, R4.Pin_1
