# Fritzing sketch id2070_I2C_due_0 (saved by Fritzing 0.9.0b)

parts:
  Part1 = Arduino Due (Rev2b)
  Part2 = Arduino Due (Rev2b)

nets:
  N1: Part1.D20/SDA3, Part2.D20/SDA3
  N2: Part1.D21/SCL3, Part2.D21/SCL3
  GND: Part1.GND, Part2.GND
