# Fritzing sketch id2071_Interrupt_multiplex_1_0 (saved by Fritzing 0.9.2b)
breadboards: 1

parts:
  Part1 = Arduino Nano (Rev3.0)
  S1 = Pushbutton [package="[THT]"]
  S2 = Pushbutton [package="[THT]"]
  D1 = Rectifier Diode [part_number=1N4001 package="300 mil [THT]"]
  D2 = Rectifier Diode [part_number=1N4001 package="300 mil [THT]"]
  R1 = Resistor [tolerance=±5% resistance=10k package=THT]
  C1 = Ceramic Capacitor [capacitance=0.1µF package="100 mil [THT, multilayer]"]
  R2 = Resistor [tolerance=±5% resistance=10k package=THT]
  R3 = Resistor [tolerance=±5% resistance=10k package=THT]
  R4 = Resistor [tolerance=±5% resistance=10k package=THT]

nets:
  N1: Part1.D2, D1.cathode, D2.cathode, C1.0, R2.Pin_0
  N2: Part1.D7, S1.Pin_3, S1.Pin_4, D2.anode, R4.Pin_0
  N3: Part1.D8, S2.Pin_4, D1.anode, R3.Pin_0
  5V: S1.Pin_1, S1.Pin_2, S2.Pin_1, S2.Pin_2
  N4: R1.Pin_0, C1.1
  GND: R1.Pin_1, R2.Pin_1, R3.Pin_1, R4.Pin_1
