# Fritzing sketch id2072_140627_2_41pm_emit_detect_LCDsignal_0 (saved by Fritzing 0.8.7b)
breadboards: 1

parts:
  Part1 = Arduino Uno (Rev3)
  Q1 = LTR-301 [package=ltr-301]
  R1 = Resistor [tolerance=±5% resistance=220 package=THT]
  D1 = LTE-302 [package=lte-302]
  R2 = Resistor [tolerance=±5% resistance=220 package=THT]
  LED1 = LED - 5mm [color="Red (633nm)" package="5 mm [THT]"]
  R3 = Resistor [tolerance=±5% resistance=220 package=THT]

nets:
  N1: Part1.A0, R1.Pin_1
  N2: Part1.GND, Q1.E, D1.C, LED1.cathode
  N3: Q1.C, R1.Pin_0
  N4: D1.A, R2.Pin_0
  N5: LED1.anode, R3.Pin_0
