# Fritzing sketch id2073_IntruderAlertV2_0 (saved by Fritzing 0.9.1b)
circuit board: 8.46667cm x 5.64444cm
breadboards: 1

parts:
  Part1 = prefix0000 [part_number=HC-SR04]
  Part2 = Arduino Mega ADK (Rev3)
  LED2 = DUO LED RG [package="5 mm [THT]"]
  R1 = Resistor [package="2512 [SMD]"]
  J1 = Piezo Speaker
  S1 = SWITCH-MOMENTARY-2 [package=tactile_switch_smd-2]

nets:
  N1: Part1.connector0, Part2.D4_PWM
  N2: Part1.connector1, Part2.GND, J1.pin1
  N3: Part1.connector2, Part2.D2_PWM
  N4: Part1.connector3, Part2.5V, R1.Pin_1, S1.2
  N5: Part2.A0, S1.1
  N6: Part2.D7_PWM, J1.pin2
  N7: Part2.D40, LED2.red_anode
  N8: Part2.D41, LED2.green_anode
  N9: LED2.common_cathode, R1.Pin_0
