# Fritzing sketch id2074_EgillOgFreyr___Arduino01_0 (saved by Fritzing 0.7.10b)
breadboards: 1

parts:
  Arduino1 = Arduino
  330 = Resistor [tolerance=±5% resistance=330 package=THT]
  LED1 = RGB LED (com. anode, rbg) [package="5 mm [THT]"]
  7_Segment1 = 7 Segment Display
  Buzzer = Piezo Speaker
  Button = Pushbutton [package="[SMD]"]
  10k = Resistor [tolerance=±5% resistance=10k package=THT]
  330_2 = Resistor [tolerance=±5% resistance=330 package=THT]
  330_3 = Resistor [tolerance=±5% resistance=330 package=THT]
  330_4 = Resistor [tolerance=±5% resistance=330 package=THT]

nets:
  N1: Arduino1.GND, LED1.common_anode, Buzzer.pin1, Button.Pin_1, Button.Pin_2
  N2: Arduino1.D12, 10k.Pin_0
  N3: Arduino1.D11, 330_3.Pin_1
  N4: Arduino1.D10, 330_4.Pin_1
  N5: Arduino1.D9, 330_2.Pin_1
  N6: Arduino1.D8, Arduino1.+5V, Button.Pin_3, Button.Pin_4
  N7: Arduino1.D7, 330.Pin_0
  N8: Arduino1.D6, 7_Segment1.Segment_G
  N9: Arduino1.D5, 7_Segment1.Segment_F
  N10: Arduino1.D4, 7_Segment1.Segment_E
  N11: Arduino1.D3, 7_Segment1.Segment_D
  N12: Arduino1.D2, 7_Segment1.Segment_C
  N13: Arduino1.D1TX, 7_Segment1.Segment_B
  N14: Arduino1.D0RX, 7_Segment1.Segment_A
  N15: 330.Pin_1, 7_Segment1.common_anode
  N16: LED1.red_cathode, 330_2.Pin_0
  N17: LED1.blue_cathode, 330_3.Pin_0
  N18: LED1.green_cathode, 330_4.Pin_0
  N19: Buzzer.pin2, 10k.Pin_1
