# Fritzing sketch id2075_Intro_curcuit_0 (saved by Fritzing 0.9.2b)
breadboards: 1

parts:
  S1 = Pushbutton [package="[THT]"]
  R1 = Resistor [tolerance=±5% resistance=220 package=THT]
  R2 = Resistor [tolerance=±5% resistance=220 package=THT]
  LED1 = LED - 5mm [color="Red (633nm)" package="5 mm [THT]"]
  LED2 = LED - 5mm [color="Red (633nm)" package="5 mm [THT]"]
  VCC1 = Battery block 9V

nets:
  N1: S1.Pin_1, S1.Pin_2, R1.Pin_0, R2.Pin_0
  N2: S1.Pin_3, S1.Pin_4, VCC1.+
  N3: R1.Pin_1, LED1.cathode
  N4: R2.Pin_1, LED2.cathode
  N5: LED1.anode, LED2.anode, VCC1.-
