# Fritzing sketch id2078_Intro_to_circuits_0 (saved by Fritzing 0.9.2b)
breadboards: 1

parts:
  VCC1 = Battery
  S1 = Pushbutton [package="[THT]"]
  R1 = Resistor [tolerance=±5% resistance=220 package=THT]
  R2 = Resistor [tolerance=±5% resistance=220 package=THT]
  LED1 = LED - 5mm [color="Red (633nm)" package="5 mm [THT]"]
  LED2 = LED - 5mm [color="Red (633nm)" package="5 mm [THT]"]

nets:
  N1: VCC1.+, S1.Pin_3, S1.Pin_4, LED1.anode, LED2.anode
  N2: S1.Pin_1, S1.Pin_2, R1.Pin_0
  N3: R2.Pin_0, LED1.cathode
  N4: R2.Pin_1, LED2.cathode
