# Fritzing sketch id2079_first_working_prototype_0 (saved by Fritzing 0.9.0b)
breadboards: 1

parts:
  Part1 = Breadboard Power Supply Board SMD [part_number="Vin = 12V"]
  R1 = Resistor [tolerance=±5% resistance=150 package=THT]
  R2 = Resistor [tolerance=±5% resistance=100 package=THT]
  U1 = HIH-4030 [part_number="Moisture Sensor" package=hih-4030]
  Q1 = npn-Powertransistor [part_number=TIP120 package="TO220 [THT]"]
  R3 = Resistor [tolerance=±5% resistance=10 power=5W package=THT]
  R4 = Resistor [tolerance=±5% resistance=028 part_number="Water Valve" package=THT]

nets:
  GND: Part1.GND, R2.Pin_0, U1.GND, Q1.emitter, R4.Pin_0
  N1: Part1.VCC, R1.Pin_1, R3.Pin_1
  N2: R1.Pin_0, R2.Pin_1, U1.VCC
  N3: U1.OUT, Q1.base
  N4: Q1.collector, R3.Pin_0, R4.Pin_1

notes:
  Voltage divider
  NOT gate
