# Fritzing sketch id207_ISProject_0 (saved by Fritzing 0.8.7b)
circuit board: 8.46667cm x 5.64444cm
breadboards: 1

parts:
  J1 = Piezo Speaker
  VCC1 = Battery
  U1 = LM 358 Dual Op-Amp [package="DIP8 [THT]"]
  C1 = Ceramic Capacitor [capacitance=100nF package="100 mil [THT, multilayer]"]
  S1 = Pushbutton [package="[THT]"]
  R1 = Resistor [tolerance=±5% resistance=1k package=THT]
  R3 = Resistor [tolerance=±5% resistance=10k package=THT]
  R2 = Resistor [tolerance=±5% resistance=1k package=THT]
  R4 = Resistor [tolerance=±20% resistance=330 package=THT]
  S2 = Pushbutton [package="[THT]"]
  S3 = Pushbutton [package="[THT]"]
  R5 = Resistor [tolerance=±5% resistance=6.8k package=THT]
  R6 = Resistor [tolerance=±5% resistance=1.5k package=THT]
  R7 = Resistor [tolerance=±5% resistance=6.8k package=THT]
  R8 = Resistor [tolerance=±5% resistance=100 package=THT]

nets:
  N1: J1.pin1, VCC1.-, U1.connector3, R2.Pin_0, R8.Pin_0
  N2: J1.pin2, U1.connector0
  N3: VCC1.+, U1.connector7, C1.1, R1.Pin_1
  N4: U1.connector1, C1.0, S1.Pin_3, S1.Pin_4, S2.Pin_1, S2.Pin_2, S3.Pin_1, S3.Pin_2
  N5: U1.connector2, R1.Pin_0, R3.Pin_1, R2.Pin_1, R6.Pin_0
  N6: S1.Pin_1, S1.Pin_2, R4.Pin_0
  N7: R3.Pin_0, R4.Pin_1
  N8: S2.Pin_3, S2.Pin_4, R7.Pin_0
  N9: S3.Pin_3, S3.Pin_4, R5.Pin_1
  N10: R5.Pin_0, R6.Pin_1
  N11: R7.Pin_1, R8.Pin_1
