# Fritzing sketch id2080_Inverter_Synth_0 (saved by Fritzing 0.7.5b)
breadboards: 1

parts:
  IC1 = Hex Inverter Schmitt Trigger SN74HC14 [package="DIP (Dual Inline)"]
  C1 = Ceramic Capacitor [capacitance=0.1µF package="100 mil [THT, multilayer]"]
  R1 = Rotary Potentiometer (Small) [maximum_resistance=100kΩ]
  VCC1 = Battery block 9V
  SPKR1 = Loudspeaker

nets:
  N1: IC1.1A, C1.1, R1.leg2
  N2: IC1.1Y, R1.wiper, SPKR1.pin2
  N3: IC1.GND, C1.0, VCC1.-, SPKR1.pin1
  N4: IC1.VCC, VCC1.+
