# Fritzing sketch id2081_zaky_0 (saved by Fritzing 0.8.5b)
breadboards: 1

parts:
  MAX_3232 = MAX3232
  IOIO = IOIO for Android
  R1 = Resistor [tolerance=±5% resistance=3.3k package=THT]
  R2 = Resistor [tolerance=±5% resistance=3.3k package=THT]
  6V = Screw terminal - 2 pins [package=THT]
  HSR-8498HB = Basic Servo
  HSR-8498HB_2 = Basic Servo

nets:
  N1: MAX_3232.connector1, R2.Pin_0
  N2: MAX_3232.connector2, R1.Pin_0
  N3: MAX_3232.connector3, R2.Pin_1, HSR-8498HB_2.pulse
  N4: MAX_3232.connector4, R1.Pin_1, HSR-8498HB.pulse
  N5: MAX_3232.connector5, IOIO.3.3V
  GND: MAX_3232.connector6, IOIO.GND, 6V.pin2, HSR-8498HB.gnd, HSR-8498HB_2.gnd
  N6: MAX_3232.connector7, IOIO.PIN3
  N7: MAX_3232.connector8, IOIO.PIN4
  N8: MAX_3232.connector9, IOIO.PIN5
  N9: MAX_3232.connector10, IOIO.PIN6
  VCC: IOIO.VCC, 6V.pin1, HSR-8498HB.vcc, HSR-8498HB_2.vcc
