# Fritzing sketch id2082_iot2_0 (saved by Fritzing 0.9.2b)
breadboards: 2

parts:
  J1 = T Cobbler Plus Cable
  LED1 = LED - 5mm [color="Red (633nm)" package="5 mm [THT]"]
  R1 = Resistor [tolerance=±5% resistance=330 package=THT]
  S1 = Pushbutton [package="[THT]"]

nets:
  N1: J1.connector0, S1.Pin_3, S1.Pin_4
  N2: J1.connector5, LED1.cathode, R1.Pin_0
  N3: J1.connector15, LED1.anode
  N4: J1.connector32, R1.Pin_1, S1.Pin_1, S1.Pin_2
