# Fritzing sketch id2083_iot1_0 (saved by Fritzing 0.9.2b)
breadboards: 2

parts:
  J2 = T Cobbler Plus Cable
  R1 = Resistor [tolerance=±5% resistance=330 package=THT]
  LED1 = LED - 5mm [color="Red (633nm)" package="5 mm [THT]"]

nets:
  N1: J2.connector1, R1.Pin_1
  N2: J2.connector14, LED1.cathode
  N3: R1.Pin_0, LED1.anode
