# Fritzing sketch id2086_Capitive_portal_with_auto_shut_off_0 (saved by Fritzing 0.9.2b)
breadboards: 1

parts:
  LED1 = LED - 5mm [color="Red (633nm)" package="5 mm [THT]"]
  S1 = Pushbutton [package="[THT]"]
  VCC1 = 4 x AAA Battery Mount
  U1 = NodeMCU
  KY-1 = keyes

nets:
  N1: LED1.cathode, U1.connector13
  N2: LED1.anode, VCC1.-, U1.connector15, KY-1.connector1, KY-1.connector2
  N3: S1.Pin_1, S1.Pin_2
  N4: S1.Pin_3, S1.Pin_4
  N5: U1.connector2, KY-1.connector0
