# Fritzing sketch id2087_RPi_Home_Automation_0 (saved by Fritzing 0.9.3b)
breadboards: 1

parts:
  U1 = RELAY [package=relay-jzc]
  Raspberry_Pi_1 = Raspberry Pi 3 [part_number=RPI-3-V1.2]
  U2 = RELAY [package=relay-jzc]
  Q1 = TRANSISTOR_NPN [package=to-92]
  D1 = Schottky Diode [part_number=1N5817 package="Melf DO-213 AB [SMD]"]
  D2 = Schottky Diode [part_number=1N5817 package="Melf DO-213 AB [SMD]"]
  Q2 = TRANSISTOR_NPN [package=to-92]
  R1 = Resistor [tolerance=±5% resistance=220 package="0402 [SMD]"]
  R2 = Resistor [tolerance=±5% resistance=220 package="0402 [SMD]"]
  Part1 = Variable Capacitor [capacitance=100nF max_capacitance=10pF min_capacitance=2pF voltage=35V]
  BAT1 = Battery Holders [package=battcom_20mm_pth]
  Part2 = Variable Capacitor [capacitance=100nF max_capacitance=10pF min_capacitance=2pF voltage=35V]
  BAT2 = Battery Holders [package=battcom_20mm_pth]

nets:
  N1: U1.COIL2, Raspberry_Pi_1.5V
  N2: U1.NO, Part2.0
  N3: U1.MAIN, BAT2.-
  N4: U1.COIL1, D2.anode, Q2.E
  N5: Raspberry_Pi_1.GIPO17, R1.Pin_0
  N6: Raspberry_Pi_1.GIPO18, R2.Pin_0
  N7: Raspberry_Pi_1.GND, U2.COIL2, Q1.C, D1.cathode, Q2.C
  N8: U2.NO, Part1.0
  N9: U2.MAIN, BAT1.-
  N10: U2.COIL1, Q1.E, D1.anode
  N11: Q1.B, R1.Pin_1
  N12: Q2.B, R2.Pin_1
  N13: Part1.1, BAT1.+
  N14: Part2.1, BAT2.+

notes:
  The battery reps the mains supply while X marks the appliance to be controlled with orange color coded wires as Live and grey as neutral.
