# Fritzing sketch id2089_ec_ph_esp32_0 (saved by Fritzing 0.9.3b)

parts:
  EC-Salinity_Probe_Interface1 = uFire_EC_Probe_Interface [chip_label="EC-Salinity Probe Interface"]
  U1 = ESP32-HiLetgo [part_number=ESP32S-HiLetgo]
  IC1 = uFire_ISE_Probe_Interface [chip_label="uFire ISE Probe Interface"]

nets:
  N1: EC-Salinity_Probe_Interface1.connector3, U1.connector0, IC1.connector3
  N2: EC-Salinity_Probe_Interface1.connector4, U1.connector7, IC1.connector4
  N3: EC-Salinity_Probe_Interface1.connector5, U1.connector30, IC1.connector5
  N4: EC-Salinity_Probe_Interface1.connector6, U1.connector37, IC1.connector6
