# Fritzing sketch id208_50mm_breakboard_0 (saved by Fritzing 0.7.4b)
breadboards: 1

parts:
  J2 = Generic_male_header___6_pins__NOSOLD [form="♂ (male)"]
  J3 = Generic_male_header___6_pins__NOSOLD [form="♂ (male)"]
  J18 = Generic_male_header___6_pins__NOSOLD [form="♂ (male)"]
  J19 = Generic_male_header___6_pins__NOSOLD [form="♂ (male)"]
  J20 = Generic_male_header___6_pins__NOSOLD [form="♂ (male)"]
  J21 = Generic_male_header___6_pins__NOSOLD [form="♂ (male)"]
  J22 = Generic_male_header___6_pins__NOSOLD [form="♂ (male)"]
  J23 = Generic_male_header___6_pins__NOSOLD [form="♂ (male)"]
  J24 = Generic_male_header___6_pins__NOSOLD [form="♂ (male)"]
  J25 = Generic_male_header___6_pins__NOSOLD [form="♂ (male)"]
  J26 = Generic_male_header___6_pins__NOSOLD [form="♂ (male)"]
  J27 = Generic_male_header___6_pins__NOSOLD [form="♂ (male)"]
  J28 = Generic_male_header___6_pins__NOSOLD [form="♂ (male)"]
  J29 = Generic_male_header___6_pins__NOSOLD [form="♂ (male)"]
  J30 = Generic_male_header___6_pins__NOSOLD [form="♂ (male)"]
  J31 = Generic_male_header___6_pins__NOSOLD [form="♂ (male)"]
  J32 = Generic_male_header___6_pins__NOSOLD [form="♂ (male)"]
  J33 = Generic_male_header___6_pins__NOSOLD [form="♂ (male)"]
  J35 = Generic_male_header___16_pins__nosold [form="♂ (male)"]
  J36 = Generic_male_header___16_pins__nosold [form="♂ (male)"]
  IC1 = SO16 [chip_label=IC spacing=300mil package=SO]
  J4 = Generic_male_header___6_pins__NOSOLD [form="♂ (male)"]
  J6 = Generic_male_header___6_pins__NOSOLD [form="♂ (male)"]
  J7 = Generic_male_header___6_pins__NOSOLD [form="♂ (male)"]
  J10 = Generic_male_header___6_pins__NOSOLD [form="♂ (male)"]
  J13 = Generic_male_header___6_pins__NOSOLD [form="♂ (male)"]
  J16 = Generic_male_header___6_pins__NOSOLD [form="♂ (male)"]
  J15 = Generic_male_header___6_pins__NOSOLD [form="♂ (male)"]
  J5 = Generic_male_header___6_pins__NOSOLD [form="♂ (male)"]
  J11 = Generic_male_header___6_pins__NOSOLD [form="♂ (male)"]
  J17 = Generic_male_header___6_pins__NOSOLD [form="♂ (male)"]
  J12 = Generic_male_header___6_pins__NOSOLD [form="♂ (male)"]
  J9 = Generic_male_header___6_pins__NOSOLD [form="♂ (male)"]
  J8 = Generic_male_header___6_pins__NOSOLD [form="♂ (male)"]
  J14 = Generic_male_header___6_pins__NOSOLD [form="♂ (male)"]
  J37 = Generic_male_header___16_pins__nosold [form="♂ (male)"]
  J38 = Generic_male_header___16_pins__nosold [form="♂ (male)"]

nets:
  N1: J2.connector0, J2.connector1, J2.connector2
  N2: J2.connector3, J2.connector4, J2.connector5
  N3: J3.connector0, J3.connector1, J3.connector2
  N4: J3.connector3, J3.connector4, J3.connector5
  N5: J18.connector0, J18.connector1, J18.connector2
  N6: J18.connector3, J18.connector4, J18.connector5, IC1.16
  N7: J19.connector0, J19.connector1, J19.connector2
  N8: J19.connector3, J19.connector4, J19.connector5, IC1.14
  N9: J20.connector0, J20.connector1, J20.connector2
  N10: J20.connector3, J20.connector4, J20.connector5, IC1.7
  N11: J21.connector0, J21.connector1, J21.connector2
  N12: J21.connector3, J21.connector4, J21.connector5, IC1.6
  N13: J22.connector0, J22.connector1, J22.connector2
  N14: J22.connector3, J22.connector4, J22.connector5, IC1.15
  N15: J23.connector0, J23.connector1, J23.connector2
  N16: J23.connector3, J23.connector4, J23.connector5, IC1.12
  N17: J24.connector0, J24.connector1, J24.connector2
  N18: J24.connector3, J24.connector4, J24.connector5, IC1.9
  N19: J25.connector0, J25.connector1, J25.connector2
  N20: J25.connector3, J25.connector4, J25.connector5, IC1.2
  N21: J26.connector0, J26.connector1, J26.connector2
  N22: J26.connector3, J26.connector4, J26.connector5, IC1.3
  N23: J27.connector0, J27.connector1, J27.connector2
  N24: J27.connector3, J27.connector4, J27.connector5, IC1.4
  N25: J28.connector0, J28.connector1, J28.connector2
  N26: J28.connector3, J28.connector4, J28.connector5, IC1.1
  N27: J29.connector0, J29.connector1, J29.connector2
  N28: J29.connector3, J29.connector4, J29.connector5, IC1.11
  N29: J30.connector0, J30.connector1, J30.connector2
  N30: J30.connector3, J30.connector4, J30.connector5, IC1.5
  N31: J31.connector0, J31.connector1, J31.connector2
  N32: J31.connector3, J31.connector4, J31.connector5, IC1.8
  N33: J32.connector0, J32.connector1, J32.connector2
  N34: J32.connector3, J32.connector4, J32.connector5, IC1.13
  N35: J33.connector0, J33.connector1, J33.connector2
  N36: J33.connector3, J33.connector4, J33.connector5, IC1.10
  N37: J35.connector0, J35.connector1, J35.connector2, J35.connector3, J35.connector4, J35.connector5, J35.connector6, J35.connector7, J35.connector8, J35.connector9, J35.connector10, J35.connector11, J35.connector12, J35.connector13, J35.connector14, J35.connector15, J37.connector9, J38.connector9
  N38: J36.connector0, J36.connector1, J36.connector2, J36.connector3, J36.connector4, J36.connector5, J36.connector6, J36.connector7, J36.connector8, J36.connector9, J36.connector10, J36.connector11, J36.connector12, J36.connector13, J36.connector14, J36.connector15, J37.connector8, J38.connector8
  N39: J4.connector0, J4.connector1, J4.connector2
  N40: J4.connector3, J4.connector4, J4.connector5
  N41: J6.connector0, J6.connector1, J6.connector2
  N42: J6.connector3, J6.connector4, J6.connector5
  N43: J7.connector0, J7.connector1, J7.connector2
  N44: J7.connector3, J7.connector4, J7.connector5
  N45: J10.connector0, J10.connector1, J10.connector2
  N46: J10.connector3, J10.connector4, J10.connector5
  N47: J13.connector0, J13.connector1, J13.connector2
  N48: J13.connector3, J13.connector4, J13.connector5
  N49: J16.connector0, J16.connector1, J16.connector2
  N50: J16.connector3, J16.connector4, J16.connector5
  N51: J15.connector0, J15.connector1, J15.connector2
  N52: J15.connector3, J15.connector4, J15.connector5
  N53: J5.connector0, J5.connector1, J5.connector2
  N54: J5.connector3, J5.connector4, J5.connector5
  N55: J11.connector0, J11.connector1, J11.connector2
  N56: J11.connector3, J11.connector4, J11.connector5
  N57: J17.connector0, J17.connector1, J17.connector2
  N58: J17.connector3, J17.connector4, J17.connector5
  N59: J12.connector0, J12.connector1, J12.connector2
  N60: J12.connector3, J12.connector4, J12.connector5
  N61: J9.connector0, J9.connector1, J9.connector2
  N62: J9.connector3, J9.connector4, J9.connector5
  N63: J8.connector0, J8.connector1, J8.connector2
  N64: J8.connector3, J8.connector4, J8.connector5
  N65: J14.connector0, J14.connector1, J14.connector2
  N66: J14.connector3, J14.connector4, J14.connector5
  N67: J37.connector0, J37.connector1, J37.connector2, J37.connector3, J37.connector4
  N68: J37.connector5, J37.connector6, J37.connector7
  N69: J37.connector10, J37.connector11, J37.connector12
  N70: J37.connector13, J37.connector14, J37.connector15
  N71: J38.connector0, J38.connector1, J38.connector2, J38.connector3, J38.connector4
  N72: J38.connector5, J38.connector6, J38.connector7
  N73: J38.connector10, J38.connector11, J38.connector12
  N74: J38.connector13, J38.connector14, J38.connector15

notes:
  1
  2
  3
  4
  5
  6
  7
  8
  12
  11
  9
  10
  16
  15
  13
  14
  A
  B
  C
  F
  D
  E
  -
  J
  I
  H
  G
  +
  L
  K
  A shameless ripoff of  Adafruit Perma-Proto Quarter-sized Breadboard PCB,
  ===
  =
  with a twist.  rd@tilde.se 20120622    License: Creative Commons Share Alike
  1 2 3 4
  5 6 7 8
  9 10 11 12
  13 14 15 16
