# Fritzing sketch id2090_IoT_Morse_Code_Emitter_Starter_Kit_0 (saved by Fritzing 0.9.3b)
breadboards: 1

parts:
  Raspberry_Pi_1 = Raspberry Pi 3 [part_number=RPI-3-V1.2]
  LED1 = smd LED [color="Red (633nm)" package="0603 [SMD]"]

nets:
  N1: Raspberry_Pi_1.GND, LED1.cathode
  N2: Raspberry_Pi_1.GIPO17, LED1.anode
