# Fritzing sketch id2091_IoTMusicBox_0 (saved by Fritzing 0.9.2b)
breadboards: 1

parts:
  Part1 = Arduino Uno (Rev3)
  Part2 = Spark Core (v1.0)
  SP1 = SPEAKER [package=pcb_mount_speaker]
  LED1 = LED - 5mm [color="Red (633nm)" package="5 mm [THT]"]
  R1 = Resistor [tolerance=±5% resistance=220 package=THT]

nets:
  N1: Part1.D8, SP1.-
  N2: Part1.D0/RX, Part2.TX
  N3: Part1.D1/TX, Part2.RX
  N4: Part1.D4, R1.Pin_1
  N5: Part2.GND, SP1.+, LED1.cathode
  N6: LED1.anode, R1.Pin_0
