# Fritzing sketch id2096_TembooYahooWeather_0 (saved by Fritzing 0.9.2b)
breadboards: 1

parts:
  LED1 = LED - 5mm [color="Red (633nm)" package="5 mm [THT]"]
  R1 = Resistor [tolerance=±5% resistance=220 package=THT]
  S1 = Pushbutton [package="[THT]"]
  R2 = Resistor [tolerance=±5% resistance=10k package=THT]
  부품1 = Arduino Yun

nets:
  N1: LED1.cathode, R1.Pin_1
  N2: LED1.anode, 부품1.D13/SCK
  N3: R1.Pin_0, R2.Pin_1, 부품1.GND
  N4: S1.Pin_1, S1.Pin_2, R2.Pin_0, 부품1.D8
  N5: S1.Pin_3, S1.Pin_4, 부품1.5V
