# Fritzing sketch id2097_IoT_Temperature_Sensor_0 (saved by Fritzing 0.9.3b)
breadboards: 1

parts:
  Part1 = Arduino Uno (Rev3)
  U1 = TMP36 [package=to-92]

nets:
  N1: Part1.A0, U1.VOUT
  5V: Part1.5V, U1.VCC
  GND: Part1.GND, U1.GND
