# Fritzing sketch id2098_IoT_Nano_DHT_11_ESP8266_01_0 (saved by Fritzing 0.9.3b)
circuit board: 8.46667cm x 5.64444cm
breadboards: 1

parts:
  VCC1 = Battery
  Componente1 = Arduino Nano (Rev3.0)
  ESP8266-01 = ESP8266_module [part_number=ESP8266]
  DHT1 = DHT11_Temperature_and_Humitidy_Sensor
  R1 = Resistor [tolerance=±5% resistance=10k package=THT]
  R2 = Resistor [tolerance=±5% resistance=220 package=THT]

nets:
  N1: VCC1.-, Componente1.GND, Componente1.D5, ESP8266-01.connector6, ESP8266-01.connector7, DHT1.connector4
  N2: VCC1.+, Componente1.D6, ESP8266-01.connector0, ESP8266-01.connector1, R1.Pin_0, R2.Pin_0
  N3: Componente1.D8, DHT1.connector2
  N4: Componente1.5V, DHT1.connector1
  N5: ESP8266-01.connector2, ESP8266-01.connector3, R1.Pin_1
  N6: ESP8266-01.connector4, ESP8266-01.connector5, R2.Pin_1
