# Fritzing sketch id209_DC_motor_0 (saved by Fritzing 0.7.4b)
breadboards: 1

parts:
  M1 = DC Motor
  Arduino1 = Arduino
  Q1 = NPN-Transistor [package="TO92 [THT]"]
  R1 = Resistor [tolerance=±5% resistance=220 package=THT]

nets:
  N1: M1.pin_1, Arduino1.+5V
  N2: M1.pin_2, Q1.E
  N3: Arduino1.D11, R1.Pin_0
  N4: Arduino1.GND, Q1.C
  N5: Q1.B, R1.Pin_1
