# Fritzing sketch id20_Workshop_05_Potentiometer_0 (saved by Fritzing 0.9.3b)
circuit board: 6.88566cm x 5.36311cm
breadboards: 2

parts:
  LED1 = LED - 5mm [color="Red (633nm)" package="5 mm [THT]"]
  LED2 = LED - 5mm [color="Green (555nm)" package="5 mm [THT]"]
  R1 = Resistor [tolerance=±5% resistance=220 package=THT]
  R2 = Resistor [tolerance=±5% resistance=220 package=THT]
  Bauteil1 = Arduino Uno (Rev3)
  R3 = Rotary Potentiometer (Small) [maximum_resistance=100kΩ package=THT]

nets:
  N1: LED1.cathode, LED2.cathode, Bauteil1.GND, R3.leg1
  N2: LED1.anode, R1.Pin_1
  N3: LED2.anode, R2.Pin_1
  N4: R1.Pin_0, Bauteil1.D10_PWM/SS
  N5: R2.Pin_0, Bauteil1.D9_PWM
  N6: Bauteil1.A0, R3.wiper
  N7: Bauteil1.5V, R3.leg2

notes:
  FLIP FLOP
