# Fritzing sketch id2101_iPCR_sketch_0 (saved by Fritzing 0.9.0b)
breadboards: 1

parts:
  Part1 = Arduino Mega 2560 (Rev3)  # not connected
  PELTIER_ELEMENT = Peltier Element  # not connected
  LCD_DISPLAY = LCD screen  # not connected
  TEMP_SENSOR = LM35 Temperature Sensor [package="TO92 [THT]"]  # not connected
  Q1 = NPN-Transistor [package="TO92 [THT]"]  # not connected
  U1 = RELAY-SOLIDSTATE [package=relay-s108t02]  # not connected
  U3 = TMP36 [package=to-92-kit]  # not connected
  Part3 = Arduino Xbee Libellium Shield
  Part2 = Arduino XBee Shield  # not connected
  U4 = XBEE-1 [package=xbee-1]
  Part4 = Thumb Joystick  # not connected
  U5 = RELAY [package=relay-t9a]  # not connected
  U6 = RELAY [package=relay-t9a-2]  # not connected
  U7 = RELAY [package=relay-jzc]  # not connected
  U8 = RELAY [package=relay-g5q]  # not connected

nets:
  N1: Part3.I/08, U4.DIO0
  N2: Part3.I/02, U4.DIO1
  N3: Part3.I/03, U4.DIO2
  N4: Part3.I/06, U4.DIO3
  N5: Part3.I/05, U4.RTS
  N6: Part3.15, U4.DIO5
  N7: Part3.14, Part3.8, U4.RES
  N8: Part3.13, U4.DIO9
  N9: Part3.I/07, U4.CTS
  N10: Part3.I/04, U4.DIO4
  GND: Part3.GND, U4.GND
  N11: Part3.9, U4.DTR
  N12: Part3.PWM1, U4.DIO11
  N13: Part3.PWM0, U4.RSSI
  N14: Part3.RST, U4.RESET
  N15: Part3.4, U4.DIO12
  N16: Part3.DIN, U4.DIN
  N17: Part3.DOUT, U4.DOUT
  +3V3: Part3.+3V3, U4.VDD
