# Fritzing sketch id2102_9led_0 (saved by Fritzing 0.9.3b)
breadboards: 1

parts:
  Součástka1 = Arduino Uno (Rev3)
  R1 = Resistor [tolerance=±5% resistance=220 package=THT]
  IR1 = TSOP312.., 314.. [package=THT]
  LED1 = RGB LED - (4 legs) [package="5 mm [THT]"]
  LED2 = RGB LED - (4 legs) [package="5 mm [THT]"]
  LED3 = RGB LED - (4 legs) [package="5 mm [THT]"]
  R2 = Resistor [tolerance=±5% resistance=220 package=THT]
  R3 = Resistor [tolerance=±5% resistance=220 package=THT]
  R4 = Resistor [tolerance=±5% resistance=220 package=THT]
  R5 = Resistor [tolerance=±5% resistance=220 package=THT]
  R6 = Resistor [tolerance=±5% resistance=220 package=THT]
  R7 = Resistor [tolerance=±5% resistance=220 package=THT]
  R8 = Resistor [tolerance=±5% resistance=220 package=THT]
  R9 = Resistor [tolerance=±5% resistance=220 package=THT]

nets:
  N1: Součástka1.D8, R5.Pin_1
  N2: Součástka1.D9_PWM, R6.Pin_1
  N3: Součástka1.D10_PWM/SS, R9.Pin_1
  N4: Součástka1.D11_PWM/MOSI, IR1.Data
  N5: Součástka1.D12/MISO, R8.Pin_1
  N6: Součástka1.D13/SCK, R7.Pin_1
  GND: Součástka1.GND, IR1.GND, LED1.common_anode, LED2.common_anode, LED3.common_anode
  N7: Součástka1.D4, R1.Pin_1
  N8: Součástka1.D5_PWM, R3.Pin_1
  N9: Součástka1.D6_PWM, R2.Pin_1
  N10: Součástka1.D7, R4.Pin_1
  N11: Součástka1.5V, IR1.Vs
  N12: R1.Pin_0, LED1.blue_cathode
  N13: LED1.red_cathode, R2.Pin_0
  N14: LED1.green_cathode, R3.Pin_0
  N15: LED2.red_cathode, R6.Pin_0
  N16: LED2.green_cathode, R5.Pin_0
  N17: LED2.blue_cathode, R4.Pin_0
  N18: LED3.red_cathode, R9.Pin_0
  N19: LED3.green_cathode, R8.Pin_0
  N20: LED3.blue_cathode, R7.Pin_0

notes:
  moje prvni zbastleni...
