# Fritzing sketch id2103_IR_RGB_Superflex_0 (saved by Fritzing 0.8.7b)
circuit board: 8cm x 2.5cm
breadboards: 1

parts:
  LED1 = Super Flux RGB LED (com. anode) [color=Blue]
  U1 = Arduino Nano (Rev3.0)
  R1 = Resistor [tolerance=±5% resistance=150 package=THT]
  R2 = Resistor [tolerance=±5% resistance=220 package=THT]
  R3 = Resistor [tolerance=±5% resistance=680 package=THT]
  IR1 = TSOP312.., 314.. [package=THT]
  R4 = Resistor [tolerance=±20% resistance=100 package=THT]
  C1 = Ceramic Capacitor [capacitance=100nF package="100 mil [THT, multilayer]"]
  C2 = Ceramic Capacitor [capacitance=100nF package="100 mil [THT, multilayer]"]

nets:
  N1: LED1.red_cathode, R1.Pin_0
  N2: LED1.blue_cathode, R2.Pin_0
  N3: LED1.green_cathode, R3.Pin_0
  5V: LED1.common_anode, U1.5V, R4.Pin_0, C2.0
  GND: U1.GND, IR1.GND, C1.0, C2.1
  N4: U1.D5, R1.Pin_1
  N5: U1.D9, R3.Pin_1
  N6: U1.D10, R2.Pin_1
  N7: U1.D11/MOSI, IR1.Data
  N8: IR1.Vs, R4.Pin_1, C1.1

notes:
  hdf-mjf.de
  IR controlled RGB LED, _Rev.A
