# Fritzing sketch id2104_motion_senser__0 (saved by Fritzing 0.9.1b)

parts:
  arduino = Arduino Uno (Rev3)
  ir_recever = Humidity Sensor - HIH-4030 Breakout
  ir_transmiter = Humidity Sensor - HIH-4030 Breakout  # not connected
  VCC1 = Battery block 9V  # not connected
  ir_transmiter_2 = Humidity Sensor - HIH-4030 Breakout  # not connected
  VCC2 = Battery block 9V  # not connected
  VCC3 = Battery block 9V  # not connected
  ir_recever_1 = Humidity Sensor - HIH-4030 Breakout
  ardunio_2 = Arduino Uno (Rev3)
  VCC4 = Battery block 9V  # not connected

nets:
  N1: arduino.D2, ir_recever.OUT
  N2: arduino.D3_PWM, ir_recever_1.OUT
  5V: arduino.5V, ir_recever.VCC
  GND: arduino.GND, ir_recever.GND
  GND_2: ir_recever_1.GND, ardunio_2.GND
  VCC: ir_recever_1.VCC, ardunio_2.5V

notes:
  power port
  maglev track
  plexi glass
  magnetick strip
