# Fritzing sketch id2105_seleccionar_con_IR_en_7segment_LED_0 (saved by Fritzing 0.9.1b)
breadboards: 1

parts:
  Parte1 = Arduino Uno (Rev3)
  IR1 = TSOP312.., 314.. [package=THT]
  R1 = Resistor [tolerance=±0.1% resistance=3.3 package="0805 [SMD]"]
  U1 = 7-SEGMENT-DISPLAY [package=7-segment-display]

nets:
  N1: Parte1.D8, U1.E
  N2: Parte1.D9_PWM, U1.B
  N3: Parte1.D12/MISO, R1.Pin_0
  N4: Parte1.GND, IR1.Vs, U1.C, U1.F
  N5: Parte1.D2, U1.G2
  N6: Parte1.D3_PWM, U1.A
  N7: Parte1.D4, U1.DP
  N8: Parte1.D5_PWM, U1.G1
  N9: Parte1.D6_PWM, U1.D
  N10: Parte1.D7, U1.G
  N11: Parte1.5V, IR1.Data
  N12: IR1.GND, R1.Pin_1
