# Fritzing sketch id2107_IR_decoder_0 (saved by Fritzing 0.9.1b)
circuit board: 8.46667cm x 5.64444cm
breadboards: 1

parts:
  IR1 = TSOP312.., 314.. [package=THT]
  Part1 = Arduino Uno (Rev3) - ICSP
  LED1 = LED - 3mm [color="Red (633nm)" package="3 mm [THT]"]
  LED2 = LED - 3mm [color="Red (633nm)" package="3 mm [THT]"]
  LED3 = LED - 3mm [color="Red (633nm)" package="3 mm [THT]"]
  LED4 = LED - 3mm [color="Red (633nm)" package="3 mm [THT]"]
  R1 = Resistor [tolerance=±5% resistance=220 package=THT]
  R2 = Resistor [tolerance=±5% resistance=220 package=THT]
  R3 = Resistor [tolerance=±5% resistance=220 package=THT]
  R4 = Resistor [tolerance=±5% resistance=220 package=THT]

nets:
  N1: IR1.GND, Part1.ICSP_MOSI, Part1.D11_PWM/MOSI
  N2: IR1.Vs, Part1.GND, LED1.cathode, LED2.cathode, LED3.cathode, LED4.cathode
  N3: IR1.Data, Part1.5V
  N4: Part1.D2, R1.Pin_1
  N5: Part1.D3_PWM, R2.Pin_1
  N6: Part1.D4, R3.Pin_1
  N7: Part1.D5_PWM, R4.Pin_1
  N8: LED1.anode, R1.Pin_0
  N9: LED2.anode, R2.Pin_0
  N10: LED3.anode, R3.Pin_0
  N11: LED4.anode, R4.Pin_0
