# Fritzing sketch id2108_Coche_control_IR_0 (saved by Fritzing 0.9.1b)
breadboards: 1

parts:
  Parte1 = Arduino Uno (Rev3)
  IC1 = L293D [package=THT]
  M1 = DC Motor
  IR1 = TSOP312.., 314.. [package=THT]

nets:
  N1: Parte1.D11_PWM/MOSI, IR1.GND
  N2: Parte1.D3_PWM, IC1.Enable_1
  N3: Parte1.5V, IC1.In_2, IC1.+Vmotor, IC1.+V, IR1.Data
  N4: Parte1.GND, IC1.In_1, IC1.0V, IR1.Vs
  N5: IC1.Out_1_(_Controlled_by_Enable_1_), M1.pin_2
  N6: IC1.Out_2_(_Controlled_by_Enable_1_), M1.pin_1
