# Fritzing sketch id2108_H_Bridge_`+2_DC (saved by Fritzing 0.4.2b)
breadboards: 1

parts:
  Arduino1 = Arduino
  Pot_2 = Rotary Potentiometer (Large) [package=THT]
  Pot_1 = Rotary Potentiometer (Large) [package=THT]
  Switch_2 = Pushbutton [package="[THT]"]
  Switch_1 = Pushbutton [package="[THT]"]
  IC1 = H-Bridge [package=THT]
  Motor_1 = DC Motor
  Motor_2 = DC Motor
  VCC_12_volts = obsolete Battery
  R3 = Resistor [resistance=10k package=THT]
  R3_2 = Resistor [resistance=10k package=THT]

nets:
  GND: Arduino1.GND, Pot_2.leg2, Pot_1.leg2, Switch_2.Pin_3, Switch_2.Pin_4, Switch_1.Pin_3, Switch_1.Pin_4, IC1.GND1, IC1.GND2, IC1.GND3, IC1.GND4, VCC_12_volts.-
  N1: Arduino1.D10, IC1.1_2EN
  N2: Arduino1.D9, IC1.3_4EN
  N3: Arduino1.D7, IC1.4A
  N4: Arduino1.D6, IC1.3A
  N5: Arduino1.D5, Switch_2.Pin_1, Switch_2.Pin_2, R3.Pin_0
  N6: Arduino1.D4, IC1.2A
  N7: Arduino1.D3, IC1.1A
  N8: Arduino1.D2, Switch_1.Pin_1, Switch_1.Pin_2, R3_2.Pin_0
  N9: Arduino1.+5V, Pot_2.leg1, Pot_1.leg1, IC1.VCC1, R3.Pin_1, R3_2.Pin_1
  N10: Arduino1.A0, Pot_1.wiper
  N11: Arduino1.A1, Pot_2.wiper
  N12: IC1.1Y, Motor_2.pin_1
  N13: IC1.2Y, Motor_2.pin_2
  N14: IC1.VCC2, VCC_12_volts.+
  N15: IC1.3Y, Motor_1.pin_2
  N16: IC1.4Y, Motor_1.pin_1
