# Fritzing sketch id2109_IR_Remote_Emulator_0 (saved by Fritzing 0.9.1b)
breadboards: 1

parts:
  Arduino1 = Arduino Mini (Rev5)
  LED1 = LEDs [package=led10mm]
  SP1 = SPEAKER [package=pcb_mount_speaker]
  R1 = Resistor [tolerance=±5% resistance=220 package=THT]
  S1 = Round Pushbutton
  VCC1 = Battery block 9V

nets:
  N1: Arduino1.GND, LED1.A, SP1.+, VCC1.-
  N2: Arduino1.D3_PWM, R1.Pin_1
  N3: Arduino1.D9_PWM, SP1.-
  N4: Arduino1.VCC, S1.leg0
  N5: LED1.C, R1.Pin_0
  N6: S1.leg1, VCC1.+

notes:
  LED IR
  Speaker 8 ohm
  Resistor 180 ohm
