# Fritzing sketch id2110_ir_remote_with_bluetooth_0 (saved by Fritzing 0.8.7b)
breadboards: 1

parts:
  Part1 = Arduino Uno (Rev3)
  LED1 = LED - 5mm [color="Red (633nm)" package="5 mm [THT]"]
  Part2 = hc-05-06
  R1 = Resistor [tolerance=±5% resistance=220 package=THT]

nets:
  N1: Part1.D2, Part2.connector14
  N2: Part1.D3_PWM, R1.Pin_1
  N3: Part1.D4, Part2.connector13
  N4: Part1.5V, Part2.connector15
  N5: Part1.GND, LED1.cathode, Part2.connector17
  N6: LED1.anode, R1.Pin_0
