# Fritzing sketch id2111_Arduino_IR_Sensor_Shield_0 (saved by Fritzing 0.9.3b)
circuit board: 6.0375cm x 3.20486cm
perfboards: 1

parts:
  Bauteil1 = Arduino Nano (Rev3.0)
  J1 = Screw terminal - 2 pins [package=THT]
  J2 = screw terminal, 3 pins
  J3 = screw terminal, 3 pins

nets:
  N1: Bauteil1.GND, J1.pin2
  N2: Bauteil1.D11/MOSI, J3.pin3
  N3: Bauteil1.VIN, J1.pin1
  N4: Bauteil1.5V, J3.pin2
  N5: Bauteil1.A2, J2.pin1
  N6: Bauteil1.A1, J2.pin2
  N7: Bauteil1.A0, J2.pin3

notes:
  RELAIS
  IR Sensor
  12V 1.5A
  ARDUINO IR SENSOR SHIELD
  IR SENSOR SHIELD
  PK ELECTRONICS 2016
