# Fritzing sketch id2112_Untitled_Sketch_21_0 (saved by Fritzing 0.9.3b)
breadboards: 1

parts:
  IR1 = TSOP312.., 314.. [package=THT]
  Q1 = NPN-Transistor [package="TO92 [THT]"]
  BAT1 = BC9VPC [package=bc9vpc]
  U1 = RELAY-SOLIDSTATE [package=relay-s108t02]

nets:
  N1: IR1.GND, Q1.E, BAT1.V-
  N2: IR1.Vs, BAT1.V+, U1.+
  N3: IR1.Data, Q1.C
  N4: Q1.B, U1.-
