# Fritzing sketch id2113_IR_sensor_0 (saved by Fritzing 0.9.3b)

parts:
  Part1 = Arduino Uno (Rev3)
  IR1 = TSOP312.., 314.. [package=THT]
  LED1 = LEDs [package=led10mm]

nets:
  N1: Part1.D11_PWM/MOSI, IR1.Data
  N2: Part1.D7, LED1.A
  N3: Part1.5V, IR1.Vs
  GND: Part1.GND, IR1.GND, LED1.C
