# Fritzing sketch id2116_Irrigator_0 (saved by Fritzing 0.9.2b)
circuit board: 13.1164cm x 8.78592cm
breadboards: 2

parts:
  Arduino_NANO = Arduino Nano (Rev3.0)
  RTC_Module = Real Time Clock Module - DS1307 RTC Breakout Board
  R1 = Resistor [tolerance=±5% resistance=220 package=THT]
  R2 = Resistor [tolerance=±5% resistance=220 package=THT]
  R3 = Resistor [tolerance=±5% resistance=10k package=THT]
  R4 = Resistor [tolerance=±5% resistance=10k package=THT]
  Button_On-PIN2_(blue_botton) = Pushbutton [package="[THT]"]
  Button_OFF-PIN3_(red_botton) = Pushbutton [package="[THT]"]
  LED1_PIN7 = LED - 5mm [color="Green (555nm)" package="5 mm [THT]"]
  LED2-PIN6 = LED - 5mm [color="Red (633nm)" package="5 mm [THT]"]
  U1 = RELAY
  U2 = RELAY
  U3 = RELAY
  RESET_(green_botton) = Pushbutton [package="[SMD]"]
  R5 = Resistor [tolerance=±5% resistance=10k package=THT]
  R6 = Resistor [tolerance=±5% resistance=10k package=THT]
  R7 = Resistor [tolerance=±5% resistance=10k package=THT]
  SET = Pushbutton [package="[SMD]"]
  Hour = Pushbutton [package="[SMD]"]
  Minute = Pushbutton [package="[SMD]"]
  Grove1 = Grove 4 Digit Display

nets:
  N1: Arduino_NANO.RESET, RESET_(green_botton).Pin_3, RESET_(green_botton).Pin_4
  GND: Arduino_NANO.GND, RTC_Module.GND, R1.Pin_0, R3.Pin_0, R4.Pin_0, RESET_(green_botton).Pin_1, RESET_(green_botton).Pin_2, R5.Pin_0, R6.Pin_0, R7.Pin_0, Grove1.GND
  N2: Arduino_NANO.D2, R3.Pin_1, Button_On-PIN2_(blue_botton).Pin_1, Button_On-PIN2_(blue_botton).Pin_2
  N3: Arduino_NANO.D3, R4.Pin_1, Button_OFF-PIN3_(red_botton).Pin_1, Button_OFF-PIN3_(red_botton).Pin_2
  N4: Arduino_NANO.D4, LED2-PIN6.cathode
  N5: Arduino_NANO.D5, LED1_PIN7.anode
  N6: Arduino_NANO.D6, U1.connector4
  N7: Arduino_NANO.D7, U2.connector4
  N8: Arduino_NANO.D8, U3.connector4
  N9: Arduino_NANO.D9, R5.Pin_1, SET.Pin_1, SET.Pin_2
  N10: Arduino_NANO.D10, R6.Pin_1, Hour.Pin_1, Hour.Pin_2
  N11: Arduino_NANO.D11/MOSI, Grove1.DIO
  N12: Arduino_NANO.D12/MISO, Grove1.CLK
  5V: Arduino_NANO.5V, RTC_Module.5V, R2.Pin_0, Button_On-PIN2_(blue_botton).Pin_3, Button_On-PIN2_(blue_botton).Pin_4, Button_OFF-PIN3_(red_botton).Pin_3, Button_OFF-PIN3_(red_botton).Pin_4, U1.connector0, U2.connector0, U3.connector0, SET.Pin_3, SET.Pin_4, Hour.Pin_3, Hour.Pin_4, Minute.Pin_3, Minute.Pin_4, Grove1.VCC
  N13: Arduino_NANO.A5, RTC_Module.SCL
  N14: Arduino_NANO.A4, RTC_Module.SDA
  N15: Arduino_NANO.D13/SCK, R7.Pin_1, Minute.Pin_1, Minute.Pin_2
  N16: R1.Pin_1, LED1_PIN7.cathode
  N17: R2.Pin_1, LED2-PIN6.anode
