# Fritzing sketch id2117_ISArduino_0 (saved by Fritzing 0.6.4b)
breadboards: 1

parts:
  Arduino1 = Arduino
  R1 = Photocell (LDR) [package=THT]
  R2 = Photocell (LDR) [package=THT]
  R3 = Resistor [tolerance=±5% resistance=4.7k package=THT]
  R4 = Resistor [tolerance=±5% resistance=4.7k package=THT]
  J1 = Basic Servo

nets:
  N1: Arduino1.D9, J1.pulse
  5V: Arduino1.+5V, R1.pin_0, R2.pin_1, J1.vcc
  GND: Arduino1.GND, R3.Pin_1, R4.Pin_0, J1.gnd
  N2: Arduino1.A0, R1.pin_1, R3.Pin_0
  N3: Arduino1.A1, R2.pin_0, R4.Pin_1
