# Fritzing sketch id2119_ArduinoISP_0 (saved by Fritzing 0.7.4b)
breadboards: 1

parts:
  VERDE = LED - 5mm [color="Orange (605nm)" package="5 mm [THT]"]
  ROJO = LED - 5mm [color="Red (633nm)" package="5 mm [THT]"]
  AMBAR = LED - 5mm [color="Green (555nm)" package="5 mm [THT]"]
  R1 = Resistor [tolerance=±5% resistance=220 package=THT]
  R2 = Resistor [tolerance=±5% resistance=220 package=THT]
  R3 = Resistor [tolerance=±5% resistance=220 package=THT]
  C1 = Electrolytic Capacitor [capacitance=10µF package="100 mil [THT, electrolytic]"]
  AT85/45 = IC, DIP package, 8 pins [chip_label=AT85 spacing=300mil]
  ArduinoISP_Shield = Arduino
  AT84/44 = IC, DIP package, 14 pins [chip_label=AT84 spacing=300mil]

nets:
  N1: VERDE.cathode, R3.Pin_1
  N2: VERDE.anode, ArduinoISP_Shield.D7
  N3: ROJO.cathode, R2.Pin_1
  N4: ROJO.anode, ArduinoISP_Shield.D8
  N5: AMBAR.cathode, R1.Pin_1
  N6: AMBAR.anode, ArduinoISP_Shield.D9
  N7: R1.Pin_0, R2.Pin_0, R3.Pin_0, C1.-, AT85/45.pin4, ArduinoISP_Shield.GND, AT84/44.pin14
  N8: C1.+, ArduinoISP_Shield.RST
  N9: AT85/45.pin1, ArduinoISP_Shield.D10, AT84/44.pin4
  N10: AT85/45.pin5, ArduinoISP_Shield.D11, AT84/44.pin7
  N11: AT85/45.pin6, ArduinoISP_Shield.D12, AT84/44.pin8
  N12: AT85/45.pin7, ArduinoISP_Shield.D13, AT84/44.pin9
  N13: AT85/45.pin8, ArduinoISP_Shield.+5V, AT84/44.pin1

notes:
  Arduino.ISP.Shield.4ATtiny
