# Fritzing sketch id211_meteo_station_0 (saved by Fritzing 0.9.2b)
breadboards: 1

parts:
  Arduino_Uno = Arduino Uno (Rev3)
  Φωτοαντίσταση = Photocell (LDR) [package=THT]
  part = Resistor [tolerance=±5% resistance=10k package=THT]
  Αισθητήρας_θερμοκρασίας = TMP36 Temperature Sensor [package="TO92 [THT]"]

nets:
  N1: Arduino_Uno.A0, Φωτοαντίσταση.pin_1, part.Pin_0
  N2: Arduino_Uno.A1, Αισθητήρας_θερμοκρασίας.Vout
  GND: Arduino_Uno.GND, part.Pin_1, Αισθητήρας_θερμοκρασίας.GND
  N3: Arduino_Uno.5V, Φωτοαντίσταση.pin_0, Αισθητήρας_θερμοκρασίας.+Vs
