# Fritzing sketch id2120_pcb_opdracht_it_0 (saved by Fritzing 0.9.3b)
circuit board: 9.19328cm x 8.34256cm
breadboards: 1

parts:
  LED1 = smd LED [color="Red (633nm)" package="0603 [SMD]"]
  S1 = Momentary Switch [package=ksa_sealed_tac_switch]
  R1 = Resistor [tolerance=±5% resistance=220 package=THT]
  C1 = Electrolytic Capacitor [capacitance=1µF package="100 mil [THT, electrolytic]"]
  R2 = Photocell (LDR) [package=THT]
  Raspberry_Pi_1 = Raspberry Pi 3 [part_number=RPI-3-V1.2]

nets:
  N1: LED1.cathode, C1.+
  N2: LED1.anode, S1.1, S1.2, S1.3, S1.4, R1.Pin_0
  N3: R1.Pin_1, Raspberry_Pi_1.5V
  N4: C1.-, R2.pin_1
  N5: R2.pin_0, Raspberry_Pi_1.GND
