# Fritzing sketch id2121_WordKlock_0 (saved by Fritzing 0.9.0b)
breadboards: 1

parts:
  Componente1 = Arduino Nano (Rev3.0)
  R1 = Resistor [tolerance=±5% resistance=10k package=THT]
  R2 = Resistor [tolerance=±5% resistance=10k package=THT]
  R3 = Resistor [tolerance=±5% resistance=10k package=THT]
  R4 = Resistor [tolerance=±5% resistance=470 package=THT]
  D1 = Rectifier Diode [part_number=1N4001 package="300 mil [THT]"]
  Componente4 = Real Time Clock Module - DS1307 RTC Breakout Board
  S1 = Pushbutton [package="[THT]"]
  S2 = Pushbutton [package="[THT]"]
  S3 = Pushbutton [package="[THT]"]
  S4 = Pushbutton [package="[THT]"]
  U1 = LCD-16X2 [package=lcd-16x2]
  LCM1602_IIC2 = generic_ic_dip_22_300mil.fzp [part_number="LCM1602 IIC" chip_label="LCM1602 IIC"]
  NEOPIXEL2 = Neopixel_Strip____Black__30_m
  Componente5 = DC-DC 5v (bottom)
  D4 = Rectifier Diode [part_number=1N4001 package="300 mil [THT]"]
  D3 = Rectifier Diode [part_number=1N4001 package="300 mil [THT]"]
  Power_plug1 = Power plug

nets:
  GND: Componente1.GND, R1.Pin_0, R2.Pin_0, R3.Pin_0, Componente4.GND, LCM1602_IIC2.connector16, NEOPIXEL2.connector3, Componente5.connector1, Componente5.connector4, Power_plug1.GND
  N1: Componente1.D6, R3.Pin_1, S2.Pin_3, S2.Pin_4
  N2: Componente1.D7, R2.Pin_1, S3.Pin_3, S3.Pin_4
  N3: Componente1.D8, R1.Pin_1, S4.Pin_3, S4.Pin_4
  N4: Componente1.D9, R4.Pin_1
  5V: Componente1.5V, Componente4.5V, S2.Pin_1, S2.Pin_2, S3.Pin_1, S3.Pin_2, S4.Pin_1, S4.Pin_2, LCM1602_IIC2.connector17, D3.cathode
  N5: Componente1.A5, Componente4.SCL, LCM1602_IIC2.connector19
  N6: Componente1.A4, Componente4.SDA, LCM1602_IIC2.connector18
  N7: R4.Pin_0, NEOPIXEL2.connector2
  N8: D1.cathode, NEOPIXEL2.connector1
  N9: D1.anode, Componente5.connector3, D3.anode
  N10: S1.Pin_1, LCM1602_IIC2.connector21
  N11: S1.Pin_3, LCM1602_IIC2.connector20
  N12: U1.VSS, LCM1602_IIC2.connector0
  N13: U1.VDD, LCM1602_IIC2.connector1
  N14: U1.VO, LCM1602_IIC2.connector2
  N15: U1.RS, LCM1602_IIC2.connector3
  N16: U1.R_W, LCM1602_IIC2.connector4
  N17: U1.E, LCM1602_IIC2.connector5
  N18: U1.DB0, LCM1602_IIC2.connector6
  N19: U1.DB1, LCM1602_IIC2.connector7
  N20: U1.DB2, LCM1602_IIC2.connector8
  N21: U1.DB3, LCM1602_IIC2.connector9
  N22: U1.DB4, LCM1602_IIC2.connector10
  N23: U1.DB5, LCM1602_IIC2.connector11
  N24: U1.DB6, LCM1602_IIC2.connector12
  N25: U1.DB7, LCM1602_IIC2.connector13
  N26: U1.A, LCM1602_IIC2.connector14
  N27: U1.K, LCM1602_IIC2.connector15
  N28: Componente5.connector0, D4.cathode
  N29: D4.anode, Power_plug1.VCC
