# Fritzing sketch id2122_iTucano_MegaChip_2_0 (saved by Fritzing 0.9.2b)
circuit board: 5.0678cm x 6.73655cm
breadboards: 1

parts:
  JP1 = Header 3 [package=molex-1x3_lock]
  JP2 = Header 3 [package=molex-1x3_lock]
  JP3 = Header 3 [package=molex-1x3_lock]
  JP4 = Header 3 [package=molex-1x3_lock]
  JP5 = Header 3 [package=molex-1x3_lock]
  JP6 = Header 3 [package=molex-1x3_lock]
  +_- = female pin header, 2 pins [form="♀ (female)"]
  1_2_3_4_5_6 = FTDI_BASIC [package=ftdi_basic]
  LED2 = LED - 5mm [color="Red (633nm)" package="5 mm [THT]"]
  LED3 = LED - 5mm [color="Green (570nm)" package="5 mm [THT]"]
  2_3 = female pin header, 2 pins [form="♀ (female)"]
  R1 = Resistor [tolerance=±5% resistance=220 package=THT]
  G_E_T_5v = FTDI_BASIC [package=ftdi_basic]
  E_T_F = FTDI_BASIC [package=ftdi_basic]
  Fotoresistenza = female pin header, 2 pins [form="♀ (female)"]
  R2 = Resistor [tolerance=±5% resistance=10k package=THT]

nets:
  N1: JP1.1, 1_2_3_4_5_6.3
  N2: JP1.2, JP2.2, JP3.2, JP4.2, JP5.2, JP6.2, +_-.pin2, G_E_T_5v.2, Fotoresistenza.pin2
  N3: JP1.3, JP2.3, JP3.3, JP4.3, JP5.3, JP6.3, +_-.pin1, R1.Pin_0, G_E_T_5v.5, R2.Pin_0
  N4: JP2.1, 1_2_3_4_5_6.2
  N5: JP3.1, 1_2_3_4_5_6.4
  N6: JP4.1, 1_2_3_4_5_6.1
  N7: JP5.1, 1_2_3_4_5_6.5
  N8: JP6.1, 1_2_3_4_5_6.6
  N9: LED2.cathode, 2_3.pin2
  N10: LED2.anode, LED3.anode, R1.Pin_1
  N11: LED3.cathode, 2_3.pin1
  N12: G_E_T_5v.3, E_T_F.1
  N13: G_E_T_5v.4, E_T_F.2
  N14: E_T_F.3, Fotoresistenza.pin1, R2.Pin_1

notes:
  HC-SR04
  iTucano MegaChip
