# Fritzing sketch id2123_iTucano_Servo_Board_0 (saved by Fritzing 0.9.2b)
circuit board: 3.48827cm x 3.14959cm
breadboards: 1

parts:
  JP1 = Header 3 [package=molex-1x3_lock]
  JP2 = Header 3 [package=molex-1x3_lock]
  JP3 = Header 3 [package=molex-1x3_lock]
  JP4 = Header 3 [package=molex-1x3_lock]
  JP5 = Header 3 [package=molex-1x3_lock]
  JP6 = Header 3 [package=molex-1x3_lock]
  1_4_2_5_3_6 = FTDI_BASIC [package=ftdi_basic]
  +_- = female pin header, 2 pins [form="♀ (female)"]

nets:
  N1: JP1.1, 1_4_2_5_3_6.1
  N2: JP1.2, JP2.2, JP3.2, JP4.2, JP5.2, JP6.2, +_-.pin1
  N3: JP1.3, JP2.3, JP3.3, JP4.3, JP5.3, JP6.3, +_-.pin2
  N4: JP2.1, 1_4_2_5_3_6.3
  N5: JP3.1, 1_4_2_5_3_6.5
  N6: JP4.1, 1_4_2_5_3_6.2
  N7: JP5.1, 1_4_2_5_3_6.4
  N8: JP6.1, 1_4_2_5_3_6.6

notes:
  iTucano's Servo Board
  www.ciaoarduino.blogspot.com
