# Fritzing sketch id2125_Nixie&IC_0 (saved by Fritzing 0.9.3b)
circuit board: 4.15177cm x 4.13779cm
breadboards: 1

parts:
  J1 = male pin header, 1 pin [form="♂ (male)"]
  J2 = female pin header, 1 pin [form="♀ (female)"]
  J3 = female pin header, 6 pins [form="♀ (female)"]
  IC1 = IC, DIP package, 16 pins [chip_label=IC]
  J4 = male alternating pin header, 1 pin [form="♂ (male)"]  # not connected
  J6 = male alternating pin header, 1 pin [form="♂ (male)"]
  J7 = male alternating pin header, 1 pin [form="♂ (male)"]
  J8 = male alternating pin header, 1 pin [form="♂ (male)"]
  J9 = male alternating pin header, 1 pin [form="♂ (male)"]
  J10 = male alternating pin header, 1 pin [form="♂ (male)"]
  J11 = male alternating pin header, 1 pin [form="♂ (male)"]
  J12 = male alternating pin header, 1 pin [form="♂ (male)"]
  J13 = male alternating pin header, 1 pin [form="♂ (male)"]  # not connected
  J15 = male alternating pin header, 1 pin [form="♂ (male)"]
  J17 = male alternating pin header, 1 pin [form="♂ (male)"]
  J18 = male alternating pin header, 1 pin [form="♂ (male)"]

nets:
  N1: J1.pin1, J2.pin1
  N2: J3.pin1, IC1.pin3
  N3: J3.pin2, IC1.pin4
  N4: J3.pin3, IC1.pin5
  N5: J3.pin4, IC1.pin6
  N6: J3.pin5, IC1.pin7
  N7: J3.pin6, IC1.pin12
  N8: IC1.pin1, J6.pin1
  N9: IC1.pin2, J7.pin1
  N10: IC1.pin8, J12.pin1
  N11: IC1.pin9, J11.pin1
  N12: IC1.pin10, J15.pin1
  N13: IC1.pin11, J17.pin1
  N14: IC1.pin13, J9.pin1
  N15: IC1.pin14, J10.pin1
  N16: IC1.pin15, J18.pin1
  N17: IC1.pin16, J8.pin1
