# Fritzing sketch id2126_SMS_v7040_video_fix_0 (saved by Fritzing 0.8.7b)
circuit board: 7.34454cm x 5.19287cm
breadboards: 1

parts:
  CXA1145P = IC, DIP package, 24 pins [chip_label="CXA1145P RGB Encoder IC"]
  B_(28) = Pad [width=6.6 height=3.18119417204301 connect=center]
  G_(27) = Pad [width=6.60166509984639 height=3.18119417204301 connect=center]
  CS_(29) = Pad [width=6.60166509984639 height=3.18119417204301 connect=center]
  R_(26) = Pad [width=6.60166509984639 height=3.18119417204301 connect=center]
  V7040 = IC, DIP package, 28 pins [chip_label="CXA1145P RGB Encoder IC"]
  C1 = Ceramic Capacitor [capacitance=100nF voltage=16V package="100 mil [THT, multilayer]"]
  C2 = Ceramic Capacitor [capacitance=100nF voltage=16V package="100 mil [THT, multilayer]"]
  C3 = Ceramic Capacitor [capacitance=100nF voltage=16V package="100 mil [THT, multilayer]"]
  R1 = Resistor [tolerance=±5% resistance=2.2k package=THT]
  R2 = Resistor [tolerance=±5% resistance=2.2k package=THT]
  R3 = Resistor [tolerance=±5% resistance=2.2k package=THT]
  R4 = Resistor [tolerance=±5% resistance=3.3k package=THT]
  R5 = Resistor [tolerance=±5% resistance=3.3k package=THT]
  R6 = Resistor [tolerance=±5% resistance=3.3k package=THT]

nets:
  N1: CXA1145P.pin1, CXA1145P.pin24, V7040.pin13, R5.Pin_0, R6.Pin_1
  N2: CXA1145P.pin2, C1.1
  N3: CXA1145P.pin3, C2.1
  N4: CXA1145P.pin4, C3.1
  N5: CXA1145P.pin12, CXA1145P.pin19, V7040.pin24, V7040.pin28
  N6: CXA1145P.pin21, V7040.pin21
  N7: CXA1145P.pin22, V7040.pin22
  N8: CXA1145P.pin23, V7040.pin23
  N9: B_(28).pad, R3.Pin_0
  N10: G_(27).pad, R2.Pin_0
  N11: CS_(29).pad, V7040.pin19, V7040.pin20
  N12: R_(26).pad, R1.Pin_0
  N13: C1.0, R1.Pin_1, R6.Pin_0
  N14: C2.0, R2.Pin_1, R5.Pin_1
  N15: C3.0, R3.Pin_1, R4.Pin_1

notes:
  315-5124
  Jailbars-Fix
  for SEGA Master System Powerbase M4
