# Fritzing sketch id2128_JayDuino_0 (saved by Fritzing 0.8.7b)
circuit board: 3.10493cm x 5.50681cm
breadboards: 1

parts:
  CPU = atmega328 [package=dip]
  PWR_5V = male pin header, 2 pins [form="♂ (male)"]
  J1 = male pin header, 5 pins [form="♂ (male)"]
  J2 = male pin header, 6 pins [form="♂ (male)"]
  J3 = male pin header, 4 pins [form="♂ (male)"]
  R1 = Resistor [tolerance=±5% resistance=220 package=THT]
  R2 = Resistor [tolerance=±5% resistance=10k package=THT]
  C1 = Electrolytic Capacitor [capacitance=100nF package="100 mil [THT, electrolytic]"]
  J4 = male pin header, 5 pins [form="♂ (male)"]
  Y1 = Resonator [frequency="16 Mhz" package=THT]
  R3 = Resistor [tolerance=±5% resistance=220 package=THT]
  LED2 = LED - 3mm [color="Red (633nm)" package="3 mm [THT]"]
  TX/RX = male pin header, 2 pins [form="♂ (male)"]
  LED1 = LED - 3mm [color="Red (633nm)" package="3 mm [THT]"]
  RST = male pin header, 1 pin [form="♂ (male)"]

nets:
  N1: CPU.RESET, R2.Pin_1, C1.+
  N2: CPU.D0_(RX), J4.pin1, TX/RX.pin1
  N3: CPU.D1_(TX), J4.pin2, TX/RX.pin2
  N4: CPU.D2, J4.pin3
  N5: CPU.D3_(PWM), J4.pin4
  N6: CPU.D4, J4.pin5
  N7: CPU.VCC, CPU.AVCC, PWR_5V.pin1, R1.Pin_0, R2.Pin_0
  GND: CPU.GND, PWR_5V.pin2, Y1.GND, LED2.cathode, LED1.cathode
  N8: CPU.XLAT1, Y1.0
  N9: CPU.XLAT2, Y1.pin_1
  N10: CPU.D5_(PWM), J3.pin1
  N11: CPU.D6_(PWM), J3.pin2
  N12: CPU.D7, J3.pin3
  N13: CPU.D8, J3.pin4
  N14: CPU.D9_(PWM), J1.pin5
  N15: CPU.D10_(PWM), J1.pin4
  N16: CPU.D11_(PWM), J1.pin3
  N17: CPU.D12, J1.pin2
  N18: CPU.D13, J1.pin1, R3.Pin_0
  N19: CPU.A0, J2.pin6
  N20: CPU.A1, J2.pin5
  N21: CPU.A2, J2.pin4
  N22: CPU.A3, J2.pin3
  N23: CPU.A4, J2.pin2
  N24: CPU.A5, J2.pin1
  N25: R1.Pin_1, LED1.anode
  N26: C1.-, RST.pin1
  N27: R3.Pin_1, LED2.anode

notes:
  +
  -
  RX
  TX
  D
  13
  12
  11
  10
  9
  A
  5
  4
  3
  2
  1
  0
  5V DC
  RST
  6
  7
  8
  Customised Bare Bones ATMega328, This is an implementation of a bare bones (or poor mans) Arduino. It provides access to all the I/O pins as well as RX/TX and RST pins., 1.0
  JayDuino328 Rev. 1.0
  R3 220
  R3 10K
  C1 100uF
  R1 220
  LED1
  LED2
  Y1 16Mhz
  VCC
  GND
  AVCC
  MISO
  MOSI
  SCK
  PIN 13
  ATMega 328
  PWR
  TIGERSHARK
  DCS CIRCUITS
  TX/RX go to corresponding pins on USB Serial interface.
