# Fritzing sketch id2129_JayDuinoTiny84_0 (saved by Fritzing 0.8.7b)
circuit board: 2.62165cm x 4.12375cm
breadboards: 1

parts:
  IC2 = IC, DIP package, 14 pins [chip_label=ATTiny24/44/84 spacing=300mil]
  J1 = male pin header, 2 pins [form="♂ (male)"]
  J2 = male pin header, 6 pins [form="♂ (male)"]
  J3 = male pin header, 6 pins [form="♂ (male)"]
  J4 = male pin header, 1 pin [form="♂ (male)"]
  C1 = Electrolytic Capacitor [capacitance=1µF package="100 mil [THT, electrolytic]"]
  LED1 = LED - 3mm [color="Red (633nm)" package="3 mm [THT]"]
  R1 = Resistor [tolerance=±5% resistance=220 package=THT]

nets:
  5V: IC2.pin1, J1.pin1, R1.Pin_0
  N1: IC2.pin2, J3.pin1
  N2: IC2.pin3, J3.pin2
  N3: IC2.pin4, J3.pin3
  N4: IC2.pin5, J3.pin4
  N5: IC2.pin6, J3.pin5
  N6: IC2.pin7, J3.pin6
  N7: IC2.pin8, J2.pin6
  N8: IC2.pin9, J2.pin5
  N9: IC2.pin10, J2.pin4
  N10: IC2.pin11, J2.pin3
  N11: IC2.pin12, J2.pin2
  N12: IC2.pin13, J2.pin1
  GND: IC2.pin14, J1.pin2, C1.+, LED1.cathode
  N13: J4.pin1, C1.-
  N14: LED1.anode, R1.Pin_1

notes:
  JayDuinoTiny84
  Rev. 1.0
  5V DC
  +
  -
  RST
  C1 100uF
  PWR
  R1 220
  ATtiny84
  VCC
  GND
  D0
  D1
  D2
  A7
  A6
  MOSI
  SCK
  MISO
  AREF
  D3
  D4
  A0
  D10
  D9
  D8
  D7
  D6
  D5
  A1
  A2
  A3
  A4
  A5
  TIGERSHARK
  DCS CIRCUIT DESIGN
