# Fritzing sketch id212_esquema_0 (saved by Fritzing 0.7.1b)
breadboards: 1

parts:
  Arduino1 = Arduino
  LCD1 = LCD screen
  R1 = Rotary Potentiometer (Small) [maximum_resistance=100kΩ]
  R2 = Resistor [tolerance=±5% resistance=1k package=THT]
  R3 = Resistor [tolerance=±5% resistance=1.5k package=THT]
  T1 = TMP36 Temperature Sensor [thermistor_type=NTC package="TO92 [THT]"]
  R6 = Photocell (LDR) [package=THT]
  R7 = Resistor [tolerance=±5% resistance=10k package=THT]
  R8 = Resistor [tolerance=±5% resistance=1.5k package=THT]

nets:
  N1: Arduino1.D12, LCD1.RS
  N2: Arduino1.D11, LCD1.E
  N3: Arduino1.D9, LCD1.LED+
  N4: Arduino1.D5, LCD1.DB4
  N5: Arduino1.D4, LCD1.DB5
  N6: Arduino1.D3, LCD1.DB6
  N7: Arduino1.D2, LCD1.DB7
  +5V: Arduino1.+5V, LCD1.VDD, R1.leg1, T1.+Vs, R6.pin_1, R8.Pin_0
  GND: Arduino1.GND, LCD1.VSS, LCD1.R/W, LCD1.LED-, R1.leg2, R2.Pin_0, T1.GND, R7.Pin_0
  N8: Arduino1.A0, T1.Vout
  N9: Arduino1.A3, R6.pin_0, R7.Pin_1
  N10: Arduino1.A5, R2.Pin_1, R3.Pin_1
  N11: LCD1.V0, R1.wiper
  N12: R3.Pin_0, R8.Pin_1
