# Fritzing sketch id2130_Jednostavni_strujni_krug_0 (saved by Fritzing 0.9.3b)
circuit board: 8.46667cm x 5.64444cm
breadboards: 1

parts:
  Baterija = Battery
  R1 = Resistor [tolerance=±5% resistance=220 package=THT]
  LED1 = LED - 5mm [color="Red (633nm)" package="5 mm [THT]"]

nets:
  N1: Baterija.-, R1.Pin_0
  N2: Baterija.+, LED1.cathode
  N3: R1.Pin_1, LED1.anode
