# Fritzing sketch id2131_JetRemote_JR0001_0 (saved by Fritzing 0.8.5b)
circuit board: 7.09789cm x 4.45911cm
breadboards: 1

parts:
  U1 = XBEE-1 [package=xbee-1_lock]
  Q1 = TRANSISTOR_NPN [package=to-92-ammo]
  U2 = V_REG_LD1117VXX [package=78xxl]
  U4 = RELAY [package=relay-g5q]
  D1 = Diode [package=diode-1n4001]
  J1 = screw terminal, 2 pins
  J2 = screw terminal, 2 pins
  R1 = Resistor [package="0402 [SMD]"]

nets:
  N1: U1.VDD, U2.OUT
  GND: U1.GND, Q1.E, U2.GND, J2.pin2
  N2: U1.DIO0, R1.Pin_0
  N3: Q1.B, R1.Pin_1
  N4: Q1.C, U4.COIL2, D1.C
  N5: U2.IN, U4.COIL1, D1.A, J2.pin1
  N6: U4.MAIN, J1.pin2
  N7: U4.NC, J1.pin1
