# Fritzing sketch id2132_Untitled_Sketch_0 (saved by Fritzing 0.9.3b)
circuit board: 2.16356cm x 4.63595cm
breadboards: 1

parts:
  Часть1 = Arduino Nano (Rev3.0)
  LED1 = LED - 5mm [color="Red (633nm)" package="5 mm [THT]"]  # not connected
  R1 = Resistor [tolerance=±5% resistance=220 package=THT]

nets:
  N1: Часть1.D4, R1.Pin_0
