# Fritzing sketch id2134_Simon_Sketch2_0 (saved by Fritzing 0.9.2b)
breadboards: 1

parts:
  LED1 = LED - 5mm [color="Green (570nm)" package="5 mm [THT]"]
  LED2 = LED - 5mm [color="Red (633nm)" package="5 mm [THT]"]
  LED4 = LED - 5mm [color="Blue (525nm)" package="5 mm [THT]"]
  SPKR1 = Loudspeaker
  Part1 = Arduino Nano (Rev3.0)
  S1 = Pushbutton [package="[THT]"]
  S2 = Pushbutton [package="[THT]"]
  S3 = Pushbutton [package="[THT]"]
  S4 = Pushbutton [package="[THT]"]
  R1 = Resistor [tolerance=±5% resistance=10k package=THT]
  R2 = Resistor [tolerance=±5% resistance=10k package=THT]
  R3 = Resistor [tolerance=±5% resistance=10k package=THT]
  R4 = Resistor [tolerance=±5% resistance=10k package=THT]
  R5 = Resistor [tolerance=±5% resistance=220 package=THT]
  R6 = Resistor [tolerance=±5% resistance=220 package=THT]
  R7 = Resistor [tolerance=±5% resistance=220 package=THT]
  R8 = Resistor [tolerance=±5% resistance=220 package=THT]
  LED3 = LED - 5mm [color="Yellow (585nm)" package="5 mm [THT]"]

nets:
  N1: LED1.cathode, LED2.cathode, LED4.cathode, SPKR1.pin1, Part1.GND, R1.Pin_1, R2.Pin_1, R3.Pin_1, R4.Pin_1, LED3.cathode
  N2: LED1.anode, R5.Pin_0
  N3: LED2.anode, R6.Pin_0
  N4: LED4.anode, R7.Pin_0
  N5: SPKR1.pin2, Part1.D4
  N6: Part1.D6, R8.Pin_1
  N7: Part1.D7, R6.Pin_1
  N8: Part1.D8, R7.Pin_1
  N9: Part1.D9, R5.Pin_1
  N10: Part1.D10, S3.Pin_3, S3.Pin_4, R3.Pin_0
  N11: Part1.D11/MOSI, S2.Pin_3, S2.Pin_4, R2.Pin_0
  N12: Part1.D12/MISO, S4.Pin_3, S4.Pin_4, R4.Pin_0
  N13: Part1.5V, S1.Pin_1, S1.Pin_2, S2.Pin_1, S2.Pin_2, S3.Pin_1, S3.Pin_2, S4.Pin_1, S4.Pin_2
  N14: Part1.D13/SCK, S1.Pin_3, S1.Pin_4, R1.Pin_0
  N15: R8.Pin_0, LED3.anode
