# Fritzing sketch id2135_jogo_da_memoria_0 (saved by Fritzing 0.9.0b)
circuit board: 7.43844cm x 5.35581cm
breadboards: 1

parts:
  Componente1 = Arduino Uno (Rev3)
  S3 = Pushbutton [package="[THT]"]
  R5 = Resistor [tolerance=±5% resistance=220 package=THT]
  LED3 = LED - 5mm [color="Green (555nm)" package="5 mm [THT]"]
  R6 = Resistor [tolerance=±5% resistance=1k package=THT]
  S4 = Pushbutton [package="[THT]"]
  R7 = Resistor [tolerance=±5% resistance=220 package=THT]
  LED4 = LED - 5mm [color="Green (555nm)" package="5 mm [THT]"]
  R8 = Resistor [tolerance=±5% resistance=1k package=THT]
  S5 = Pushbutton [package="[THT]"]
  R9 = Resistor [tolerance=±5% resistance=220 package=THT]
  LED5 = LED - 5mm [color="Green (555nm)" package="5 mm [THT]"]
  R10 = Resistor [tolerance=±5% resistance=1k package=THT]
  R11 = Resistor [tolerance=±5% resistance=220 package=THT]
  R12 = Resistor [tolerance=±5% resistance=1k package=THT]
  LED6 = LED - 5mm [color="Green (555nm)" package="5 mm [THT]"]
  S6 = Pushbutton [package="[THT]"]
  R3 = Resistor [tolerance=±5% resistance=220 package=THT]
  S2 = Pushbutton [package="[THT]"]
  R4 = Resistor [tolerance=±5% resistance=1k package=THT]
  LED2 = LED - 5mm [color="Green (555nm)" package="5 mm [THT]"]

nets:
  N1: Componente1.D8, Componente1.D2, Componente1.D3_PWM, S3.Pin_3, S3.Pin_4, R5.Pin_1, R3.Pin_1, S2.Pin_3, S2.Pin_4, R4.Pin_1
  N2: Componente1.D9_PWM, R6.Pin_1
  N3: Componente1.D10_PWM/SS, R8.Pin_1
  N4: Componente1.D11_PWM/MOSI, R10.Pin_1
  N5: Componente1.D12/MISO, R12.Pin_1
  N6: Componente1.GND, R5.Pin_0, LED3.cathode, R7.Pin_0, LED4.cathode, R9.Pin_0, LED5.cathode, R11.Pin_0, LED6.cathode, R3.Pin_0, LED2.cathode
  N7: Componente1.D4, S4.Pin_3, S4.Pin_4, R7.Pin_1
  N8: Componente1.D5_PWM, S5.Pin_3, S5.Pin_4, R9.Pin_1
  N9: Componente1.D6_PWM, R11.Pin_1, S6.Pin_3, S6.Pin_4
  N10: Componente1.5V, S3.Pin_1, S3.Pin_2, S4.Pin_1, S4.Pin_2, S5.Pin_1, S5.Pin_2, S6.Pin_1, S6.Pin_2, S2.Pin_1, S2.Pin_2, R4.Pin_0, LED2.anode
  N11: LED3.anode, R6.Pin_0
  N12: LED4.anode, R8.Pin_0
  N13: LED5.anode, R10.Pin_0
  N14: R12.Pin_0, LED6.anode
