# Fritzing sketch id2137_Joydelox_v111_0 (saved by Fritzing 0.9.0b)
circuit board: 3.1cm x 4.3cm
breadboards: 1

parts:
  J1 = double row female pin header, 10 pins [form="♀ (female)"]
  S1 = Pushbutton [package="[THT]"]
  S2 = Pushbutton [package="[THT]"]
  S3 = Pushbutton [package="[THT]"]
  S4 = Pushbutton [package="[THT]"]
  S5 = Pushbutton [package="[THT]"]
  R1 = Resistor [tolerance=±5% resistance=22k package=THT]
  R3 = Resistor [tolerance=±5% resistance=4.7k package=THT]
  R4 = Resistor [tolerance=±5% resistance=2.2k package=THT]
  R5 = Resistor [tolerance=±5% resistance=1.2k package=THT]
  R6 = Resistor [tolerance=±5% resistance=4.7k package=THT]
  S6 = Pushbutton [package=THT]
  R2 = Resistor [tolerance=±5% resistance=10k package=THT]
  S7 = Toggle Switch [package=THT]
  VCC1 = Battery
  J2 = Piezo Speaker
  R7 = Resistor [tolerance=±5% resistance=1M package=THT]

nets:
  N1: J1.pin1, S6.leg1
  N2: J1.pin2, J1.pin9, R1.Pin_1, R3.Pin_1, R4.Pin_1, R5.Pin_1, S6.leg0, R2.Pin_1, VCC1.-, J2.pin1, R7.Pin_1
  N3: J1.pin5, S7.L2
  N4: J1.pin7, J2.pin2, R7.Pin_0
  N5: J1.pin8, S1.Pin_3, S1.Pin_4, S2.Pin_3, S2.Pin_4, S3.Pin_3, S3.Pin_4, S4.Pin_3, S4.Pin_4, S5.Pin_3, S5.Pin_4, R6.Pin_0
  N6: J1.pin10, R6.Pin_1
  N7: S1.Pin_1, S1.Pin_2, R1.Pin_0
  N8: S2.Pin_1, S2.Pin_2, R2.Pin_0
  N9: S3.Pin_1, S3.Pin_2, R3.Pin_0
  N10: S4.Pin_1, S4.Pin_2, R4.Pin_0
  N11: S5.Pin_1, S5.Pin_2, R5.Pin_0
  N12: S7.COM, VCC1.+

notes:
  RES
  GND
  RX
  TX
  +5V
  5VOUT
  IO2
  IO1
  3.3V
  +
  -
  Joydelox v1.1.1
  RESET
  POWER
  http://www.kreativekorp.com/
  Mount         S1-S5        on back
  P-
  P+
  PIEZO
