# Fritzing sketch id2138_joymega_0 (saved by Fritzing 0.9.1b)
circuit board: 4.29575cm x 3.19223cm
breadboards: 1

parts:
  Q1 = NPN-Transistor [package="TO92 [THT]"]
  R1 = Resistor [tolerance=±5% resistance=220 package=THT]
  R2 = Resistor [tolerance=±5% resistance=220 package=THT]
  X1 = DB9 Connector [package=db9]
  X2 = DB9 Connector [package=db9]

nets:
  N1: Q1.E, R2.Pin_1, X2.7
  N2: Q1.B, R1.Pin_1
  N3: Q1.C, X1.9, X2.8
  N4: R1.Pin_0, X1.8
  N5: R2.Pin_0, X1.7, X2.9
  N6: X1.1, X2.1
  N7: X1.2, X2.2
  N8: X1.3, X2.3
  N9: X1.4, X2.4
  N10: X1.5, X2.5
  N11: X1.6, X2.6
