# Fritzing sketch id2139_Joy_Mouse_0 (saved by Fritzing 0.9.3b)
breadboards: 1

parts:
  Composant1 = Arduino Micro (Rev3)
  Composant2 = Thumb Joystick
  S1 = Pushbutton [package="[SMD]"]
  S2 = Pushbutton [package="[SMD]"]
  S3 = Pushbutton [package="[SMD]"]
  S4 = Pushbutton [package="[SMD]"]

nets:
  N1: Composant1.D2/SDA, Composant2.SEL
  GND: Composant1.D3/SCL, Composant1.D4_PWM/A6, Composant1.D5_PWM, Composant1.D6_PWM/A7, Composant1.GND, Composant2.GND, S1.Pin_3, S1.Pin_4, S2.Pin_3, S2.Pin_4, S3.Pin_3, S3.Pin_4, S4.Pin_3, S4.Pin_4
  5V: Composant1.5V, Composant2.VCC
  N2: Composant1.A1, Composant2.VERT
  N3: Composant1.A0, Composant2.HORZ
  N4: S1.Pin_1, S1.Pin_2
  N5: S2.Pin_1, S2.Pin_2
  N6: S3.Pin_1, S3.Pin_2
  N7: S4.Pin_1, S4.Pin_2
