# Fritzing sketch id213_A._Tec_RGB_Christmas_0 (saved by Fritzing 0.7.12b)
breadboards: 2

parts:
  ATMEGA328 = atmega328 [package=dip]
  Power_plug1 = Power plug
  Y1 = Resonator [frequency="16 Mhz" package=THT]
  S1 = Toggle Switch [package=THT]
  U2 = Voltage Regulator - 5V [package="TO220 [THT]"]
  0_1uF = Ceramic Capacitor [capacitance=0.1µF package="100 mil [THT, multilayer]"]
  0_1uF_2 = Ceramic Capacitor [capacitance=0.1µF package="100 mil [THT, multilayer]"]
  J1 = female pin header, 8 pins [form="♀ (female)"]
  LED1 = RGB LED (com. cathode, rbg) [package="5 mm [THT]"]
  LED2 = RGB LED (com. cathode, rbg) [package="5 mm [THT]"]
  LED3 = RGB LED (com. cathode, rbg) [package="5 mm [THT]"]
  LED4 = RGB LED (com. cathode, rbg) [package="5 mm [THT]"]
  LED5 = RGB LED (com. cathode, rbg) [package="5 mm [THT]"]
  LED6 = RGB LED (com. cathode, rbg) [package="5 mm [THT]"]
  LED7 = RGB LED (com. cathode, rbg) [package="5 mm [THT]"]
  LED8 = RGB LED (com. cathode, rbg) [package="5 mm [THT]"]
  LED9 = RGB LED (com. cathode, rbg) [package="5 mm [THT]"]
  LED10 = RGB LED (com. cathode, rbg) [package="5 mm [THT]"]
  LED11 = RGB LED (com. cathode, rbg) [package="5 mm [THT]"]

nets:
  N1: ATMEGA328.D0_(RX), LED1.common_cathode
  N2: ATMEGA328.D1_(TX), LED2.common_cathode
  N3: ATMEGA328.D2, LED3.common_cathode
  N4: ATMEGA328.D3_(PWM), LED4.common_cathode
  N5: ATMEGA328.D4, LED5.common_cathode
  5V: ATMEGA328.VCC, ATMEGA328.AVCC, U2.output_voltage, 0_1uF_2.0, J1.pin1
  GND: ATMEGA328.GND, Power_plug1.GND, Y1.GND, U2.GND, 0_1uF.1, 0_1uF_2.1, J1.pin2
  N6: ATMEGA328.XLAT1, Y1.pin_1
  N7: ATMEGA328.XLAT2, Y1.0
  N8: ATMEGA328.D5_(PWM), LED6.common_cathode
  N9: ATMEGA328.D6_(PWM), LED7.common_cathode
  N10: ATMEGA328.D7, LED8.common_cathode
  N11: ATMEGA328.D8, LED9.common_cathode
  N12: ATMEGA328.D9_(PWM), LED10.common_cathode
  N13: ATMEGA328.D10_(PWM), LED11.common_cathode
  N14: ATMEGA328.D11_(PWM), LED1.blue_anode, LED2.blue_anode, LED3.blue_anode, LED4.blue_anode, LED5.blue_anode, LED6.blue_anode, LED7.blue_anode, LED8.blue_anode, LED9.blue_anode, LED10.blue_anode, LED11.blue_anode
  N15: ATMEGA328.D12, LED1.green_anode, LED2.green_anode, LED3.green_anode, LED4.green_anode, LED5.green_anode, LED6.green_anode, LED7.green_anode, LED8.green_anode, LED9.green_anode, LED10.green_anode, LED11.green_anode
  N16: ATMEGA328.D13, LED1.red_anode, LED2.red_anode, LED3.red_anode, LED4.red_anode, LED5.red_anode, LED6.red_anode, LED7.red_anode, LED8.red_anode, LED9.red_anode, LED10.red_anode, LED11.red_anode
  N17: ATMEGA328.A0, J1.pin8
  N18: ATMEGA328.A1, J1.pin7
  N19: ATMEGA328.A2, J1.pin6
  N20: ATMEGA328.A3, J1.pin5
  N21: ATMEGA328.A4, J1.pin4
  N22: ATMEGA328.A5, J1.pin3
  9V: Power_plug1.VCC, S1.L1
  N23: S1.COM, U2.input_voltage, 0_1uF.0

notes:
  A. Tec
  RGB Christmas
  v1.0
  GND
  5v
  A5
  A4
  A3
  A2
  A1
  A0
  design by:
  Ari E. Hansen
