# Fritzing sketch id2141_Untitled_Sketch_0 (saved by Fritzing 0.9.1b)

parts:
  Part1 = Thumb Joystick
  Part2 = Arduino Uno (Rev3)

nets:
  GND: Part1.GND, Part2.GND
  N1: Part1.SEL, Part2.A2
  N2: Part1.VERT, Part2.A0
  VCC: Part1.VCC, Part2.5V
