# Fritzing sketch id2142_Joystick_LED_RGB_0 (saved by Fritzing 0.9.2b)
circuit board: 8.46667cm x 5.64444cm
breadboards: 1

parts:
  LED1 = RGB LED (com. cathode, rgb) [package="5 mm [THT]"]
  R1 = Resistor [tolerance=±5% resistance=220 package=THT]
  Parte2 = Thumb Joystick
  Parte1 = Arduino Uno (Rev3) - ICSP
  R3 = Resistor [tolerance=±5% resistance=220 package=THT]
  R4 = Resistor [tolerance=±5% resistance=220 package=THT]

nets:
  N1: LED1.red_anode, R4.Pin_1
  GND: LED1.common_cathode, Parte2.GND, Parte1.GND
  N2: LED1.green_anode, R1.Pin_1
  N3: LED1.blue_anode, R3.Pin_1
  N4: R1.Pin_0, Parte1.D5_PWM
  N5: Parte2.HORZ, Parte1.A0
  N6: Parte2.VERT, Parte1.A1
  VCC: Parte2.VCC, Parte1.5V
  N7: Parte1.D4, R3.Pin_0
  N8: Parte1.D6_PWM, R4.Pin_0
