# Fritzing sketch id2143_juego_con_dos_leds_adicional_0 (saved by Fritzing 0.9.3b)
breadboards: 1

parts:
  LED1 = LED - 5mm [color="Red (633nm)" package="5 mm [THT]"]
  LED2 = LED - 5mm [color="Green (570nm)" package="5 mm [THT]"]
  R1 = Resistor [tolerance=±5% resistance=220 package=THT]
  R2 = Resistor [tolerance=±5% resistance=220 package=THT]
  Componente1 = Arduino Mega 2560 (Rev3)

nets:
  N1: LED1.cathode, Componente1.D13_PWM
  N2: LED1.anode, R2.Pin_0
  N3: LED2.cathode, Componente1.D10_PWM
  N4: LED2.anode, R1.Pin_0
  N5: R1.Pin_1, R2.Pin_1, Componente1.GND
