# Fritzing sketch id214_A4988_0 (saved by Fritzing 0.9.3b)
breadboards: 1

parts:
  J1 = STM32 Nucleo boards
  Pololu_A1 = Pololu A4988 [package=SO16]
  C1 = Electrolytic Capacitor [capacitance=1µF package="100 mil [THT, electrolytic]"]
  M2 = Stepper Motor - Bipolar

nets:
  N1: J1.D8, Pololu_A1.DIR
  N2: J1.D9_PWM, Pololu_A1.STEP
  N3: J1.D10_PWM/SS, Pololu_A1.ENABLE
  5V: J1.5V, Pololu_A1.MS1, Pololu_A1.MS3, Pololu_A1.VDD
  GND: J1.GND, Pololu_A1.GND, C1.-
  N4: Pololu_A1.RESET, Pololu_A1.SLEEP
  N5: Pololu_A1.1B, M2.D
  N6: Pololu_A1.1A, M2.B
  N7: Pololu_A1.2A, M2.C
  N8: Pololu_A1.2B, M2.A
  N9: Pololu_A1.VMOT, C1.+

notes:
  Power supply
  8-35V
