# Fritzing sketch id2150_JUEGOS_DE_LUCES_DESPACITO_TANIA_CONZA_0 (saved by Fritzing 0.9.3b)
breadboards: 1

parts:
  Parte1 = Arduino Uno (Rev3)
  LED4 = LED - 5mm [color="Red (633nm)" package="5 mm [THT]"]
  LED12 = smd LED [color="Yellow (585nm)" package="1206 [SMD]"]
  LED13 = smd LED [color="Green (555nm)" package="1206 [SMD]"]
  S1 = Pushbutton [package="[THT]"]
  R1 = Resistor [tolerance=±5% resistance=220 package=THT]
  R2 = Resistor [tolerance=±5% resistance=220 package=THT]
  R3 = Resistor [tolerance=±5% resistance=220 package=THT]
  R4 = Resistor [tolerance=±5% resistance=220 package=THT]
  LED14 = smd LED [color="Green (555nm)" package="1206 [SMD]"]
  R5 = Resistor [tolerance=±5% resistance=220 package=THT]
  LED15 = smd LED [color="Yellow (585nm)" package="1206 [SMD]"]
  R6 = Resistor [tolerance=±5% resistance=220 package=THT]
  LED16 = LED - 5mm [color="Red (633nm)" package="5 mm [THT]"]
  LED18 = smd LED [color="Yellow (585nm)" package="1206 [SMD]"]
  LED19 = smd LED [color="Green (555nm)" package="1206 [SMD]"]
  R10 = Resistor [tolerance=±5% resistance=220 package=THT]  # not connected
  R11 = Resistor [tolerance=±5% resistance=220 package=THT]

nets:
  N1: Parte1.D8, R11.Pin_0
  N2: Parte1.D13/SCK, S1.Pin_3, S1.Pin_4
  N3: Parte1.D2, R1.Pin_0
  N4: Parte1.D3_PWM, R2.Pin_0
  N5: Parte1.D4, R3.Pin_0
  N6: Parte1.D5_PWM, R4.Pin_0
  N7: Parte1.D6_PWM, R5.Pin_0
  N8: Parte1.D7, R6.Pin_0
  N9: Parte1.GND, LED4.cathode, LED12.cathode, LED13.cathode, S1.Pin_1, S1.Pin_2, LED14.cathode, LED15.cathode, LED16.cathode, LED18.cathode, LED19.cathode
  N10: LED4.anode, R3.Pin_1
  N11: LED12.anode, R2.Pin_1
  N12: R5.Pin_1, LED15.anode
  N13: LED18.anode, R11.Pin_1
