# Fritzing sketch id2152_PAOLO_2_Sketch_0 (saved by Fritzing 0.9.3b)
breadboards: 1

parts:
  LED1 = LED - 5mm [color="Red (633nm)" package="5 mm [THT]"]
  LED2 = LED - 5mm [color="Orange (612nm)" package="5 mm [THT]"]
  LED3 = LED - 5mm [color="Green (555nm)" package="5 mm [THT]"]
  Componente1 = Arduino Mega 2560 (Rev3)
  R1 = Resistor [tolerance=±5% resistance=220 package=THT]

nets:
  N1: LED1.cathode, LED2.cathode, LED3.cathode, R1.Pin_1
  N2: LED1.anode, Componente1.D13_PWM
  N3: LED2.anode, Componente1.D12_PWM
  N4: LED3.anode, Componente1.D10_PWM
