# Fritzing sketch id2155_juego_salta_dustin_0 (saved by Fritzing 0.9.2b)
breadboards: 1

parts:
  Parte1 = Arduino Uno (Rev3)
  LCD1 = LCD screen
  S1 = Pushbutton [package="[THT]"]

nets:
  N1: Parte1.D9_PWM, LCD1.E
  N2: Parte1.D11_PWM/MOSI, LCD1.RS
  N3: Parte1.D2, S1.Pin_1, S1.Pin_2
  N4: Parte1.D3_PWM, LCD1.DB7
  N5: Parte1.D4, LCD1.DB6
  N6: Parte1.D5_PWM, LCD1.DB5
  N7: Parte1.D6_PWM, LCD1.DB4
  5V: Parte1.5V, LCD1.VDD
  GND: Parte1.GND, LCD1.VSS, LCD1.V0, LCD1.R/W, LCD1.LED-, S1.Pin_3, S1.Pin_4
