# Fritzing sketch id215_Arduino_A4988_Single_Stepper_Wiring_0 (saved by Fritzing 0.8.7b)
perfboards: 1

parts:
  MD09B1 = A4988 Stepper Motor Driver Carrier
  J1 = Screw terminal - 2 pins [package=THT]
  C3 = Capacitor Polarized [package=panasonic_c]
  JP3 = Header 8 [package=1x08_smd]
  부품1 = Arduino Uno (Rev3) - ICSP
  M1 = Stepper Motor - Bipolar
  JP4 = Header 8 [package=1x08_smd]
  JP6 = Header 1 [package=1x01_offset]
  JP7 = Header 1 [package=1x01_offset]
  JP8 = Header 1 [package=1x01_offset]  # not connected
  JP9 = Header 1 [package=1x01_offset]  # not connected
  JP10 = Header 1 [package=1x01_offset]
  JP11 = Header 1 [package=1x01_offset]  # not connected
  JP12 = Header 1 [package=1x01_offset]
  JP13 = Header 1 [package=1x01_offset]
  JP14 = Header 1 [package=1x01_offset]  # not connected
  JP15 = Header 1 [package=1x01_offset]
  JP16 = Header 1 [package=1x01_offset]  # not connected
  JP17 = Header 1 [package=1x01_offset]  # not connected
  JP18 = Header 1 [package=1x01_offset]
  JP19 = Header 1 [package=1x01_offset]  # not connected
  JP20 = Header 1 [package=1x01_offset]  # not connected
  JP21 = Header 1 [package=1x01_offset]  # not connected

nets:
  N1: MD09B1.Enable, 부품1.D6_PWM, JP4.1
  N2: MD09B1.MS1, JP4.2, JP6.1
  N3: MD09B1.MS2, JP4.3, JP10.1
  N4: MD09B1.MS3, JP4.4, JP7.1
  N5: MD09B1.RESET, MD09B1.SLEEP, JP4.5, JP4.6
  N6: MD09B1.STEP, 부품1.D5_PWM, JP4.7
  N7: MD09B1.DIR, 부품1.D4, JP4.8
  N8: MD09B1.VMOT, JP3.1
  N9: MD09B1.GROUND#141, J1.pin2, C3.-, JP3.2
  N10: MD09B1.OUT_2B, JP3.3, M1.A
  N11: MD09B1.OUT_2A, JP3.4, M1.C
  N12: MD09B1.OUT_1A, JP3.5, M1.B
  N13: MD09B1.OUT_1B, JP3.6, M1.D
  N14: MD09B1.VDD, JP3.7
  N15: MD09B1.GROUND#147, JP3.8
  N16: J1.pin1, C3.+, 부품1.VIN, JP15.1
  N17: 부품1.5V, JP13.1
  N18: 부품1.GND, JP12.1, JP18.1

notes:
  motor power supply
  8-35V
