# Fritzing sketch id2160_jukebox_0 (saved by Fritzing 0.8.3b)
breadboards: 1

parts:
  Componente1 = Arduino Uno (Rev3)
  J1 = Piezo Speaker
  7_Segment1 = 7 Segment Display
  S1 = Pushbutton [package="[THT]"]
  S2 = Pushbutton [package="[THT]"]
  R3 = Resistor [tolerance=±1% resistance=10k package=THT]
  R2 = Resistor [tolerance=±5% resistance=10k package=THT]
  R4 = Resistor [tolerance=±5% resistance=470 package=THT]

nets:
  N1: Componente1.ICSP_MISO, Componente1.D12/MISO, S1.Pin_3, S1.Pin_4, R3.Pin_1
  N2: Componente1.ICSP_MOSI, Componente1.D11_PWM/MOSI, S2.Pin_3, S2.Pin_4, R2.Pin_1
  N3: Componente1.GND, R3.Pin_0, R2.Pin_0, R4.Pin_1
  N4: Componente1.D13/SCK, J1.pin2
  N5: Componente1.D4, 7_Segment1.Segment_C
  N6: Componente1.D5_PWM, 7_Segment1.Segment_D
  N7: Componente1.D6_PWM, 7_Segment1.Segment_E
  N8: Componente1.5V, S1.Pin_1, S1.Pin_2, S2.Pin_1, S2.Pin_2
  N9: 7_Segment1.common_anode, R4.Pin_0
