# Fritzing sketch id2161_jukebox_plus_0 (saved by Fritzing 0.8.3b)
breadboards: 1

parts:
  Part1 = Arduino Uno (Rev3)
  LCD1 = LCD screen
  R1 = Trimmer Potentiometer [maximum_resistance=10kΩ package=THT]
  R2 = Resistor [tolerance=±5% resistance=220 package=THT]
  R3 = Resistor [tolerance=±5% resistance=220 package=THT]
  S1 = Pushbutton [package="[SMD]"]
  S2 = Pushbutton [package="[THT]"]
  S3 = Pushbutton [package="[THT]"]
  R4 = Resistor [tolerance=±5% resistance=220 package=THT]
  J1 = Piezo Speaker

nets:
  GND: Part1.GND, LCD1.VSS, R1.leg2, R2.Pin_0, R3.Pin_0, R4.Pin_0, J1.pin1
  N1: Part1.D8, R2.Pin_1, S2.Pin_1, S2.Pin_2
  N2: Part1.D9_PWM, R3.Pin_1, S1.Pin_1, S1.Pin_2
  N3: Part1.D11_PWM/MOSI, LCD1.E
  N4: Part1.D12/MISO, LCD1.RS
  N5: Part1.D13/SCK, J1.pin2
  N6: Part1.D2, LCD1.DB7
  N7: Part1.D3_PWM, LCD1.DB6
  N8: Part1.D4, LCD1.DB5
  N9: Part1.D5_PWM, LCD1.DB4
  N10: Part1.D7, S3.Pin_1, S3.Pin_2, R4.Pin_1
  5V: Part1.5V, LCD1.VDD, R1.leg1, S1.Pin_3, S1.Pin_4, S2.Pin_3, S2.Pin_4, S3.Pin_3, S3.Pin_4
  N11: LCD1.V0, R1.wiper
