# Fritzing sketch id2163_K3NG_keyer_0 (saved by Fritzing 0.8.7b)
circuit board: 8.46667cm x 5.64444cm
breadboards: 1

parts:
  Composant1 = Arduino Uno (Rev3)
  R1 = Trimmer Potentiometer [maximum_resistance=10kΩ package=THT]
  Q1 = NPN-Transistor [package="TO92 [THT]"]
  LED1 = LED - 5mm [color="Red (633nm)" package="5 mm [THT]"]
  J1 = Piezo Speaker
  U1 = AUDIO-JACK2 [package=audio-jack-3.5mm-smd]
  R2 = Resistor [tolerance=±5% resistance=560 package=THT]
  R3 = Resistor [tolerance=±5% resistance=560 package=THT]
  R4 = Resistor [tolerance=±5% resistance=560 package=THT]
  SPKR1 = Loudspeaker
  R5 = Resistor [tolerance=±5% resistance=560 package=THT]
  Q2 = NPN-Transistor [package="TO92 [THT]"]
  U2 = AUDIO-JACK2 [package=audio-jack-3.5mm-smd]

nets:
  N1: Composant1.A0, R1.wiper
  N2: Composant1.D11_PWM/MOSI, R5.Pin_1
  N3: Composant1.D3_PWM, U1.SLEEVE
  N4: Composant1.D4, LED1.anode, J1.pin2
  N5: Composant1.D5_PWM, U1.RSH
  N6: Composant1.5V, R1.leg1
  N7: Composant1.GND, R1.leg2, Q1.E, J1.pin1, U1.RING, R2.Pin_0, SPKR1.pin1, Q2.C, U2.TSH
  N8: Composant1.VIN, R3.Pin_1
  N9: Q1.B, R4.Pin_0
  N10: Q1.C, R3.Pin_0
  N11: LED1.cathode, R2.Pin_1
  N12: R5.Pin_0, Q2.B
  N13: Q2.E, U2.TIP

notes:
  TX key 1
  Left/Right Paddle
