# Fritzing sketch id2164_Physics_Beer_Pong_Kate_Morrissey_0 (saved by Fritzing 0.9.0b)
breadboards: 1

parts:
  J1 = Basic Force Sensing Resistor (FSR) [package=THT]
  J2 = Basic Force Sensing Resistor (FSR) [package=THT]
  J3 = Basic Force Sensing Resistor (FSR) [package=THT]
  J4 = Basic Force Sensing Resistor (FSR) [package=THT]
  J5 = Basic Force Sensing Resistor (FSR) [package=THT]
  Part1 = Arduino Uno (Rev3)
  J6 = Piezo Speaker
  Part2 = Rotoshield - Motor driver shield for Arduino

nets:
  N1: J1.pin_0, Part1.A5/SCL, Part2.A_IN_5
  N2: J1.pin_1, J2.pin_1, J3.pin_1, J4.pin_1, J5.pin_1, Part1.D10_PWM/SS, J6.pin2
  N3: J2.pin_0, Part1.A4/SDA, Part2.A_IN_4
  N4: J3.pin_0, Part1.A3, Part2.A_IN_3
  N5: J4.pin_0, Part1.A2, Part2.A_IN_2
  N6: J5.pin_0, Part1.A1, Part2.A_IN_1
  GND: Part1.GND, J6.pin1, Part2.GND
