# Fritzing sketch id2165_elektronik_0 (saved by Fritzing 0.9.3b)

parts:
  Parça1 = Arduino Mega 2560 (Rev3)
  LCD1 = LCD screen
  T1 = LM35 Temperature Sensor [package="TO92 [THT]"]
  RHT1 = Humidity and Temperature Sensor RHT03
  IC1 = DS1302 [package="SO8 [SMD]"]
  S1 = SWITCH-MOMENTARY-2 [package=tactile_switch_tall]
  U1 = RELAY [package=relay-t9a-2]
  U2 = RELAY [package=relay-t9a-2]
  J1 = Basic Servo
  R2 = Resistor [tolerance=±5% resistance=220 package="0805 [SMD]"]
  M1 = DC Motor
  Power_plug1 = Power plug
  R3 = Resistor [tolerance=±5% resistance=10k package="0805 [SMD]"]
  R4 = Resistor [tolerance=±5% resistance=220 package="0603 [SMD]"]

nets:
  N1: Parça1.A4, S1.1, R4.Pin_1
  N2: Parça1.A5, T1.Vout
  GND: Parça1.GND, LCD1.VSS, LCD1.LED-, T1.GND, RHT1.GND_2, IC1.0V, U1.COIL2, U2.COIL2, J1.gnd, R2.Pin_0, M1.pin_2, Power_plug1.GND, R4.Pin_0
  N3: Parça1.D13_PWM, LCD1.RS
  N4: Parça1.D12_PWM, LCD1.E
  N5: Parça1.D11_PWM, LCD1.DB4
  N6: Parça1.D10_PWM, LCD1.DB5
  N7: Parça1.D9_PWM, LCD1.DB6
  N8: Parça1.D8_PWM, LCD1.DB7
  5V: Parça1.5V, LCD1.VDD, LCD1.LED+, T1.+Vs, RHT1.Vcc, IC1.+V, S1.2, U1.MAIN, R3.Pin_0
  N9: Parça1.D2_PWM, RHT1.Data-signal
  N10: Parça1.D3_PWM, J1.pulse
  N11: Parça1.D5_PWM, IC1.CE_-_Chip_Enable
  N12: Parça1.D6_PWM, IC1.I/O_-_SPI_Data_In/Out
  N13: Parça1.D7_PWM, IC1.SCLK_-_SPI_Clock
  N14: Parça1.D22, U1.COIL1
  N15: Parça1.D23, U2.COIL1
  N16: LCD1.V0, R3.Pin_1
  N17: U1.NO, R2.Pin_1
  VCC: U2.MAIN, J1.vcc, Power_plug1.VCC
  N18: U2.NO, M1.pin_1
