# Fritzing sketch id2167_KBM_DS_Mk1_83teI31_0 (saved by Fritzing 0.9.3b)
circuit board: 12.5cm x 12.5cm
perfboards: 1

parts:
  NE556 = 556 [package=dil14]
  S1 = Pushbutton [package=THT]
  R9 = Resistor [tolerance=±5% resistance=2k package=THT]
  LED1 = LED - 5mm [color="Blue (470nm)" package="5 mm [THT]"]
  J1 = Screw terminal - 2 pins [package=THT]
  C5 = Electrolytic Capacitor [capacitance=0.22mF voltage=10V package="200 mil [THT, electrolytic]"]
  C20 = Electrolytic Capacitor [capacitance=10µF package="100 mil [THT, electrolytic]"]
  RV2 = Rotary Potentiometer (Small) [maximum_resistance=150kΩ package=THT]
  R4 = Resistor [tolerance=±5% resistance=10k package=THT]
  U2 = prefix0000VR7809 [part_number=7809]
  R3 = Resistor [tolerance=±5% resistance=100 package=THT]
  R5 = Rotary Potentiometer (Small) [maximum_resistance=10kΩ package=THT]
  R12 = Resistor [tolerance=±5% resistance=15k package=THT]
  R7 = Rotary Potentiometer (Small) [maximum_resistance=1kΩ package=THT]
  R8 = Resistor [tolerance=±5% resistance=220 package=THT]
  C21 = Electrolytic Capacitor [capacitance=10µF package="100 mil [THT, electrolytic]"]
  C22 = Electrolytic Capacitor [capacitance=100nF package="100 mil [THT, electrolytic]"]
  R1 = Resistor [tolerance=±5% resistance=56k package=THT]
  R8_2 = Resistor [tolerance=±5% resistance=10k package=THT]
  R7_2 = Resistor [tolerance=±5% resistance=10k package=THT]
  C3 = Electrolytic Capacitor [capacitance=100µF package="100 mil [THT, electrolytic]"]
  switch1 = Rotary Switch2 3x4
  Out = NJ2FD-V
  Speed_ON/OFF = Toggle Switch [package=THT]
  D1 = Rectifier Diode [part_number=1N4001 package="300 mil [THT]"]
  R13 = Resistor [tolerance=±5% resistance=1k package=THT]
  S2 = Pushbutton [package="[THT]"]
  R14 = Resistor [tolerance=±5% resistance=1k package=THT]

nets:
  N1: NE556.DIS, R4.Pin_1, R3.Pin_0
  N2: NE556.THR, NE556.TRIG, C20.+, Speed_ON/OFF.COM
  N3: NE556.RST, NE556.VCC, S1.leg1, R9.Pin_1, R3.Pin_1, R1.Pin_0, switch1.connector3, switch1.connector11, switch1.connector12, R14.Pin_1
  N4: NE556.OUT, D1.cathode
  N5: NE556.GND, LED1.cathode, J1.pin2, C5.-, U2.connector1, R12.Pin_0, C21.-, C3.-, Out.connector2
  N6: NE556.TRIG2, NE556.THR2, R7.leg2, C21.+
  N7: NE556.OUT2, C22.+
  N8: NE556.RST2, switch1.connector14
  N9: NE556.CV2, switch1.connector13
  N10: NE556.DIS2, R8.Pin_0, R1.Pin_1
  N11: S1.leg0, U2.connector2
  N12: R9.Pin_0, LED1.anode
  N13: J1.pin1, C5.+, U2.connector0
  N14: C20.-, Speed_ON/OFF.L2, S2.Pin_3, S2.Pin_4
  N15: RV2.leg1, R4.Pin_0
  N16: RV2.leg2, Speed_ON/OFF.L1
  N17: R5.leg1, R12.Pin_1, C22.-
  N18: R5.leg2, Out.connector3
  N19: R7.leg1, R8.Pin_1
  N20: R8_2.Pin_0, switch1.connector8, switch1.connector9
  N21: R8_2.Pin_1, R7_2.Pin_1, switch1.connector5, switch1.connector6
  N22: R7_2.Pin_0, switch1.connector1, switch1.connector2
  N23: C3.+, switch1.connector4, switch1.connector7, R13.Pin_0
  N24: D1.anode, R13.Pin_1, S2.Pin_1, S2.Pin_2, R14.Pin_0
