# Fritzing sketch id2168_KBM_DS_Mk1_HgJmHTE_0 (saved by Fritzing 0.9.3b)
circuit board: 12.5cm x 12.5cm
perfboards: 1

parts:
  NE556 = 556 [package=dil14]
  S1 = Pushbutton [package=THT]
  R9 = Resistor [tolerance=±5% resistance=2k package=THT]
  LED1 = LED - 5mm [color="Blue (470nm)" package="5 mm [THT]"]
  J1 = Screw terminal - 2 pins [package=THT]
  C1 = Electrolytic Capacitor [capacitance=0.22mF voltage=10V package="200 mil [THT, electrolytic]"]
  C20 = Electrolytic Capacitor [capacitance=10µF package="100 mil [THT, electrolytic]"]
  RV1 = Rotary Potentiometer (Small) [maximum_resistance=150kΩ package=THT]
  R3 = Resistor [tolerance=±5% resistance=100 package=THT]
  U2 = prefix0000VR7809 [part_number=7809]
  R4 = Resistor [tolerance=±5% resistance=220 package=THT]
  R5 = Rotary Potentiometer (Small) [maximum_resistance=10kΩ package=THT]
  R12 = Resistor [tolerance=±5% resistance=15k package=THT]
  R7 = Rotary Potentiometer (Small) [maximum_resistance=1kΩ package=THT]
  R8 = Resistor [tolerance=±5% resistance=220 package=THT]
  C21 = Electrolytic Capacitor [capacitance=10µF package="100 mil [THT, electrolytic]"]
  C22 = Electrolytic Capacitor [capacitance=100nF package="100 mil [THT, electrolytic]"]
  R1 = Resistor [tolerance=±5% resistance=56k package=THT]
  R8_2 = Resistor [tolerance=±5% resistance=10k package=THT]
  R7_2 = Resistor [tolerance=±5% resistance=10k package=THT]  # not connected
  C3 = Electrolytic Capacitor [capacitance=100µF package="100 mil [THT, electrolytic]"]
  switch1 = Rotary Switch2 3x4
  Out = NJ2FD-V
  Speed_ON/OFF = Toggle Switch [package=THT]

nets (from the schematic view):
  N1: NE556.DIS, R3.Pin_1, R4.Pin_0
  N2: NE556.THR, NE556.TRIG, C20.+, Speed_ON/OFF.COM
  N3: NE556.RST, NE556.VCC, S1.leg1, R9.Pin_1, R4.Pin_1, switch1.connector12
  N4: NE556.GND, LED1.cathode, J1.pin2, C1.-, C20.-, U2.connector1, R12.Pin_0, C21.-, C3.-, Out.connector2, Speed_ON/OFF.L2
  N5: NE556.TRIG2, NE556.THR2, R7.leg2, C21.+
  N6: NE556.OUT2, C22.+
  N7: NE556.RST2, switch1.connector14
  N8: NE556.CV2, switch1.connector13
  N9: NE556.DIS2, R8.Pin_0, R1.Pin_1
  N10: S1.leg0, U2.connector2
  N11: R9.Pin_0, LED1.anode
  N12: J1.pin1, C1.+, U2.connector0
  N13: RV1.leg1, R3.Pin_0
  N14: RV1.leg2, Speed_ON/OFF.L1
  N15: R5.leg1, R12.Pin_1, C22.-
  N16: R5.leg2, Out.connector3
  N17: R7.leg1, R8.Pin_1
  N18: R1.Pin_0, switch1.connector10, switch1.connector11
  N19: R8_2.Pin_0, switch1.connector9
  N20: C3.+, switch1.connector7

notes:
  S1= Switch On/Off
  R5= Volume
  OUT= Jack 6.35 sur chassis
