# Fritzing sketch id2169_Taschenlampe_0 (saved by Fritzing 0.8.5b)
circuit board: 2.44759cm x 1.38895cm
breadboards: 1

parts:
  R1 = Resistor [tolerance=±5% resistance=100 package=THT]
  LED1 = LED - 5mm [color="Red (633nm)" package="5 mm [THT]"]
  IC1 = Voltage Regulator [package=to-220-alt]
  J2 = female pin header, 1 pin [form="♀ (female)"]
  J1 = female pin header, 1 pin [form="♀ (female)"]
  S3 = Pushbutton [package=THT]

nets:
  N1: R1.Pin_0, IC1.GND, J2.pin1
  N2: R1.Pin_1, LED1.cathode
  N3: LED1.anode, S3.leg0
  N4: IC1.IN, J1.pin1
  N5: IC1.OUT, S3.leg1

notes:
  2014
  GK&Mo
