# Fritzing sketch id216_STEPER_MOTOR_DRIVER_002_0 (saved by Fritzing 0.9.2b)
perfboards: 1

parts:
  MD09B1 = A4988 Stepper Motor Driver Carrier
  C1 = Electrolytic Capacitor [capacitance=1µF package="100 mil [THT, electrolytic]"]  # not connected
  J1 = Screw terminal - 2 pins [package=THT]
  J2 = Screw terminal - 2 pins [package=THT]  # not connected
  J3 = Screw terminal - 2 pins [package=THT]
  Power_plug1 = Power plug  # not connected
  J4 = Screw terminal - 2 pins [package=THT]
  J5 = Screw terminal - 2 pins [package=THT]
  Power_plug2 = Power plug
  J8 = Screw terminal - 2 pins [package=THT]  # not connected
  J9 = Screw terminal - 2 pins [package=THT]

nets:
  N1: MD09B1.RESET, MD09B1.SLEEP
  N2: MD09B1.STEP, J1.pin2
  N3: MD09B1.DIR, J1.pin1
  N4: MD09B1.VMOT, J9.pin1
  N5: MD09B1.GROUND#141, J9.pin2
  N6: MD09B1.OUT_2B, J4.pin1
  N7: MD09B1.OUT_2A, J4.pin2
  N8: MD09B1.OUT_1A, J5.pin1
  N9: MD09B1.OUT_1B, J5.pin2
  VDD: MD09B1.VDD, J3.pin2, Power_plug2.VCC
  N10: MD09B1.GROUND#147, J3.pin1, Power_plug2.GND

notes:
  5V
  12 V
  12V
  EXTRA HEDERS
  STEP/DIR
  A+A-B+B-
