# Fritzing sketch id2170_keypad2_0 (saved by Fritzing 0.7.11b)
breadboards: 1

parts:
  S1 = Pushbutton [package="[THT]"]
  S2 = Pushbutton [package="[THT]"]
  S3 = Pushbutton [package="[THT]"]
  S4 = Pushbutton [package="[THT]"]
  S5 = Pushbutton [package="[THT]"]
  R1 = Resistor [tolerance=±5% resistance=10k package=THT]
  R2 = Resistor [tolerance=±5% resistance=10k package=THT]
  R3 = Resistor [tolerance=±5% resistance=10k package=THT]
  R4 = Resistor [tolerance=±5% resistance=10k package=THT]
  R5 = Resistor [tolerance=±5% resistance=10k package=THT]
  U1 = mystery part, 12 pins [chip_label=?]
  IC1 = IC, DIP package, 14 pins [chip_label=IC]

nets:
  N1: S1.Pin_1, S1.Pin_2, R5.Pin_1
  5V: S1.Pin_3, S1.Pin_4, S2.Pin_3, S2.Pin_4, S3.Pin_3, S3.Pin_4, S4.Pin_3, S4.Pin_4, S5.Pin_3, S5.Pin_4, U1.pin6, U1.pin7, U1.pin8, U1.pin9, U1.pin10, U1.pin12, IC1.pin1, IC1.pin3, IC1.pin5, IC1.pin9, IC1.pin11, IC1.pin14
  N2: S2.Pin_1, S2.Pin_2, R4.Pin_1
  N3: S3.Pin_1, S3.Pin_2, R3.Pin_1
  N4: S4.Pin_1, S4.Pin_2, R2.Pin_1
  N5: S5.Pin_1, S5.Pin_2, R1.Pin_1
  GND: R1.Pin_0, R2.Pin_0, R3.Pin_0, R4.Pin_0, R5.Pin_0, U1.pin11, IC1.pin7
  N6: U1.pin1, IC1.pin2
  N7: U1.pin2, IC1.pin4
  N8: U1.pin3, IC1.pin6
  N9: U1.pin4, IC1.pin8
  N10: U1.pin5, IC1.pin10

notes:
  Pin 1 - 5 SW Inverted 5 - 10 SW 11 GND 12 VCC
  Elkhan Julian B 2013
  Keypad, Elkhan Julian Brillianshah, v1
