# Fritzing sketch id2171_Science_Fair_Schematic_0 (saved by Fritzing 0.9.1b)
breadboards: 1

parts:
  Part1 = Arduino Uno (Rev3)
  J1 = Piezo Speaker
  J2 = Infrared Proximity Sensor
  VCC1 = Battery block 9V  # not connected
  U1 = BUTTONPAD-4X4 [package=buttonpad-4x4-special]

nets:
  N1: Part1.D8, U1.G$3_GRN
  N2: Part1.D9_PWM, J1.pin2
  N3: Part1.D10_PWM/SS, J2.Vout
  GND: Part1.GND, J1.pin1, J2.GND
  N4: Part1.D2, U1.G$2_GND
  N5: Part1.D3_PWM, U1.G$2_GRN
  N6: Part1.D4, U1.G$1_GRN
  N7: Part1.D5_PWM, U1.G$1_GND
  N8: Part1.D6_PWM, U1.G$3_BLU
  N9: Part1.D7, U1.G$3_RED
  5V: Part1.5V, J2.Vcc
