# Fritzing sketch id2173_KILO_MUX_SHIELD_v1_0 (saved by Fritzing 0.9.1b)
circuit board: 13.1075cm x 6.21001cm
breadboards: 1

parts:
  IC2 = IC, DIP package, 24 pins [chip_label=IC]
  RX_TX = female pin header, 2 pins [form="♀ (female)"]
  J18 = shrouded pin header, 10 pins [form="♂ (shrouded male)"]
  J19 = shrouded pin header, 10 pins [form="♂ (shrouded male)"]
  J20 = shrouded pin header, 10 pins [form="♂ (shrouded male)"]
  J21 = shrouded pin header, 10 pins [form="♂ (shrouded male)"]
  IC4 = IC, DIP package, 24 pins [chip_label=IC]
  U1 = 74HC595 [package="DIP16 [THT]"]
  U2 = 74HC595 [package="DIP16 [THT]"]
  J22 = shrouded pin header, 10 pins [form="♂ (shrouded male)"]
  J23 = shrouded pin header, 10 pins [form="♂ (shrouded male)"]
  Parte1 = Arduino Uno (Rev3) - ICSP
  A5_A4_A3_A2 = female pin header, 4 pins [form="♀ (female)"]
  Out_-_In = female pin header, 2 pins [form="♀ (female)"]
  Out_-_In1 = female pin header, 2 pins [form="♀ (female)"]
  MIDI_OUT = Audio Jack (TRS) 3.5mm [package="4Ucon 08780 [THT]"]
  MIDI_IN = Audio Jack (TRS) 3.5mm [package="4Ucon 08780 [THT]"]
  6N138 = IC, DIP package, 8 pins [chip_label=IC]
  R20 = Resistor [tolerance=±5% resistance=220 package=THT]
  R17 = Resistor [tolerance=±5% resistance=220 package=THT]
  D1 = Rectifier Diode [part_number=1N4148 package="300 mil [THT]"]
  R18 = Resistor [tolerance=±5% resistance=1.8k package=THT]
  C4 = Ceramic Capacitor [capacitance=100nF package="200 mil [THT, multilayer]"]
  C3 = Ceramic Capacitor [capacitance=100nF package="100 mil [THT, multilayer]"]
  C2 = Ceramic Capacitor [capacitance=100nF package="100 mil [THT, multilayer]"]
  C1 = Ceramic Capacitor [capacitance=100nF package="100 mil [THT, multilayer]"]
  D2_D3 = female pin header, 2 pins [form="♀ (female)"]
  R19 = Resistor [tolerance=±5% resistance=220 package=THT]
  Sensor_Ultrasónico_HC-SR04 = female pin header, 4 pins [form="♀ (female)"]

nets:
  MUXB: IC2.pin1, Parte1.A1
  N1: IC2.pin2, J18.pin9
  N2: IC2.pin3, J18.pin8
  N3: IC2.pin4, J18.pin7
  N4: IC2.pin5, J18.pin6
  N5: IC2.pin6, J18.pin5
  N6: IC2.pin7, J18.pin4
  N7: IC2.pin8, J18.pin3
  N8: IC2.pin9, J18.pin2
  S0: IC2.pin10, IC4.pin10, Parte1.D4
  S1: IC2.pin11, IC4.pin11, Parte1.D5_PWM
  GND: IC2.pin12, IC2.pin15, J18.pin1, J19.pin1, J20.pin1, J21.pin1, IC4.pin12, IC4.pin15, U1.GND, U1.OE, U2.GND, U2.OE, J22.pin6, J23.pin6, Parte1.GND, MIDI_OUT.Sleeve, MIDI_IN.Sleeve, 6N138.pin5, C4.0, C3.0, C2.0, C1.0, Sensor_Ultrasónico_HC-SR04.pin4
  S3: IC2.pin13, IC4.pin13, Parte1.D7
  S2: IC2.pin14, IC4.pin14, Parte1.D6_PWM
  N9: IC2.pin16, J19.pin9
  N10: IC2.pin17, J19.pin8
  N11: IC2.pin18, J19.pin7
  N12: IC2.pin19, J19.pin6
  N13: IC2.pin20, J19.pin5
  N14: IC2.pin21, J19.pin4
  N15: IC2.pin22, J19.pin3
  N16: IC2.pin23, J19.pin2
  5V: IC2.pin24, J18.pin10, J19.pin10, J20.pin10, J21.pin10, IC4.pin24, U1.MR, U1.VCC, U2.MR, U2.VCC, Parte1.5V, 6N138.pin8, R18.Pin_0, C4.1, C3.1, C2.1, C1.1, R19.Pin_0, Sensor_Ultrasónico_HC-SR04.pin1
  N17: RX_TX.pin1, Parte1.D0/RX, Out_-_In1.pin2
  N18: RX_TX.pin2, Parte1.D1/TX, Out_-_In1.pin1
  N19: J20.pin2, IC4.pin9
  N20: J20.pin3, IC4.pin8
  N21: J20.pin4, IC4.pin7
  N22: J20.pin5, IC4.pin6
  N23: J20.pin6, IC4.pin5
  N24: J20.pin7, IC4.pin4
  N25: J20.pin8, IC4.pin3
  N26: J20.pin9, IC4.pin2
  N27: J21.pin2, IC4.pin23
  N28: J21.pin3, IC4.pin22
  N29: J21.pin4, IC4.pin21
  N30: J21.pin5, IC4.pin20
  N31: J21.pin6, IC4.pin19
  N32: J21.pin7, IC4.pin18
  N33: J21.pin8, IC4.pin17
  N34: J21.pin9, IC4.pin16
  MUXA: IC4.pin1, Parte1.A0
  N35: U1.Q1, J22.pin3
  N36: U1.Q2, J22.pin2
  N37: U1.Q3, J22.pin1
  N38: U1.Q4, J22.pin10
  N39: U1.Q5, J22.pin9
  N40: U1.Q6, J22.pin8
  N41: U1.Q7, J22.pin7
  N42: U1.Q7', U2.DS
  SH_CP: U1.SH_CP, U2.SH_CP, Parte1.D10_PWM/SS
  ST_CP: U1.ST_CP, U2.ST_CP, Parte1.D9_PWM
  DS: U1.DS, Parte1.D8
  N43: U1.Q0, J22.pin4
  N44: U2.Q1, J23.pin3
  N45: U2.Q2, J23.pin2
  N46: U2.Q3, J23.pin1
  N47: U2.Q4, J23.pin10
  N48: U2.Q5, J23.pin9
  N49: U2.Q6, J23.pin8
  N50: U2.Q7, J23.pin7
  N51: U2.Q0, J23.pin4
  N52: Parte1.A2, A5_A4_A3_A2.pin4
  N53: Parte1.A3, A5_A4_A3_A2.pin3
  N54: Parte1.A4/SDA, A5_A4_A3_A2.pin2
  N55: Parte1.A5/SCL, A5_A4_A3_A2.pin1
  ECHO: Parte1.D12/MISO, Sensor_Ultrasónico_HC-SR04.pin3
  TRIGGER: Parte1.D13/SCK, Sensor_Ultrasónico_HC-SR04.pin2
  N56: Parte1.D2, D2_D3.pin1
  N57: Parte1.D3_PWM, D2_D3.pin2
  N58: Out_-_In.pin1, R20.Pin_0
  N59: Out_-_In.pin2, 6N138.pin6, R18.Pin_1
  N60: MIDI_OUT.Ring, R20.Pin_1
  N61: MIDI_OUT.Tip, R19.Pin_1
  N62: MIDI_IN.Ring, 6N138.pin3, D1.anode
  N63: MIDI_IN.Tip, R17.Pin_0
  N64: 6N138.pin2, R17.Pin_1, D1.cathode

notes:
  (4067)
  A
  B
  C
  D
  (595)
  YTX
  ISP HEADER
  US
  KILO-MUX
