# Fritzing sketch id2174_KILO_MUX_SHIELD_v2_0 (saved by Fritzing 0.9.1b)
circuit board: 15.2089cm x 5.95983cm
breadboards: 1

parts:
  IC2 = IC, DIP package, 24 pins [chip_label=IC]
  J14 = female pin header, 3 pins [form="♀ (female)"]
  J17 = female pin header, 2 pins [form="♀ (female)"]
  J18 = shrouded pin header, 10 pins [form="♂ (shrouded male)"]
  J19 = shrouded pin header, 10 pins [form="♂ (shrouded male)"]
  J20 = shrouded pin header, 10 pins [form="♂ (shrouded male)"]
  J21 = shrouded pin header, 10 pins [form="♂ (shrouded male)"]
  IC4 = IC, DIP package, 24 pins [chip_label=IC]
  U1 = 74HC595 [package="DIP16 [THT]"]
  U2 = 74HC595 [package="DIP16 [THT]"]
  R1 = Resistor [tolerance=±5% resistance=220 package=THT]
  R2 = Resistor [tolerance=±5% resistance=220 package=THT]
  R3 = Resistor [tolerance=±5% resistance=220 package=THT]
  R4 = Resistor [tolerance=±5% resistance=220 package=THT]
  R5 = Resistor [tolerance=±5% resistance=220 package=THT]
  R6 = Resistor [tolerance=±5% resistance=220 package=THT]
  R7 = Resistor [tolerance=±5% resistance=220 package=THT]
  R8 = Resistor [tolerance=±5% resistance=220 package=THT]
  R9 = Resistor [tolerance=±5% resistance=220 package=THT]
  R10 = Resistor [tolerance=±5% resistance=220 package=THT]
  R11 = Resistor [tolerance=±5% resistance=220 package=THT]
  R12 = Resistor [tolerance=±5% resistance=220 package=THT]
  R13 = Resistor [tolerance=±5% resistance=220 package=THT]
  R14 = Resistor [tolerance=±5% resistance=220 package=THT]
  R15 = Resistor [tolerance=±5% resistance=220 package=THT]
  J22 = shrouded pin header, 10 pins [form="♂ (shrouded male)"]
  J23 = shrouded pin header, 10 pins [form="♂ (shrouded male)"]
  R16 = Resistor [tolerance=±5% resistance=680 package=THT]
  Parte1 = Arduino Uno (Rev3) - ICSP

nets:
  N1: IC2.pin1, Parte1.A1
  N2: IC2.pin2, J18.pin9
  N3: IC2.pin3, J18.pin8
  N4: IC2.pin4, J18.pin7
  N5: IC2.pin5, J18.pin6
  N6: IC2.pin6, J18.pin5
  N7: IC2.pin7, J18.pin4
  N8: IC2.pin8, J18.pin3
  N9: IC2.pin9, J18.pin2
  N10: IC2.pin10, IC4.pin10, Parte1.D2
  N11: IC2.pin11, IC4.pin11, Parte1.D3_PWM
  GND: IC2.pin12, IC2.pin15, J18.pin1, J19.pin1, J20.pin1, J21.pin1, IC4.pin12, IC4.pin15, U1.GND, U1.OE, U2.GND, U2.OE, J22.pin6, J23.pin6, Parte1.GND
  N12: IC2.pin13, IC4.pin13, Parte1.D5_PWM
  N13: IC2.pin14, IC4.pin14, Parte1.D4
  N14: IC2.pin16, J19.pin9
  N15: IC2.pin17, J19.pin8
  N16: IC2.pin18, J19.pin7
  N17: IC2.pin19, J19.pin6
  N18: IC2.pin20, J19.pin5
  N19: IC2.pin21, J19.pin4
  N20: IC2.pin22, J19.pin3
  N21: IC2.pin23, J19.pin2
  5V: IC2.pin24, J18.pin10, J19.pin10, J20.pin10, J21.pin10, IC4.pin24, U1.MR, U1.VCC, U2.MR, U2.VCC, Parte1.5V
  N22: J14.pin1, Parte1.A5/SCL
  N23: J14.pin2, Parte1.A4/SDA
  N24: J14.pin3, Parte1.A3
  N25: J17.pin1, Parte1.D0/RX
  N26: J17.pin2, Parte1.D1/TX
  N27: J20.pin2, IC4.pin9
  N28: J20.pin3, IC4.pin8
  N29: J20.pin4, IC4.pin7
  N30: J20.pin5, IC4.pin6
  N31: J20.pin6, IC4.pin5
  N32: J20.pin7, IC4.pin4
  N33: J20.pin8, IC4.pin3
  N34: J20.pin9, IC4.pin2
  N35: J21.pin2, IC4.pin23
  N36: J21.pin3, IC4.pin22
  N37: J21.pin4, IC4.pin21
  N38: J21.pin5, IC4.pin20
  N39: J21.pin6, IC4.pin19
  N40: J21.pin7, IC4.pin18
  N41: J21.pin8, IC4.pin17
  N42: J21.pin9, IC4.pin16
  N43: IC4.pin1, Parte1.A0
  N44: U1.Q1, R2.Pin_1
  N45: U1.Q2, R3.Pin_1
  N46: U1.Q3, R4.Pin_1
  N47: U1.Q4, R5.Pin_1
  N48: U1.Q5, R7.Pin_1
  N49: U1.Q6, R6.Pin_1
  N50: U1.Q7, R8.Pin_1
  N51: U1.Q7', U2.DS
  N52: U1.SH_CP, U2.SH_CP, Parte1.ICSP_MISO, Parte1.D12/MISO
  N53: U1.ST_CP, U2.ST_CP, Parte1.D9_PWM
  N54: U1.DS, Parte1.D8
  N55: U1.Q0, R1.Pin_1
  N56: U2.Q1, R13.Pin_1
  N57: U2.Q2, R14.Pin_1
  N58: U2.Q3, R12.Pin_1
  N59: U2.Q4, R11.Pin_1
  N60: U2.Q5, R15.Pin_1
  N61: U2.Q6, R10.Pin_1
  N62: U2.Q7, R16.Pin_1
  N63: U2.Q0, R9.Pin_1
  N64: R1.Pin_0, J22.pin1
  N65: R2.Pin_0, J22.pin10
  N66: R3.Pin_0, J22.pin2
  N67: R4.Pin_0, J22.pin9
  N68: R5.Pin_0, J22.pin3
  N69: R6.Pin_0, J22.pin4
  N70: R7.Pin_0, J22.pin8
  N71: R8.Pin_0, J22.pin7
  N72: R9.Pin_0, J23.pin1
  N73: R10.Pin_0, J23.pin4
  N74: R11.Pin_0, J23.pin3
  N75: R12.Pin_0, J23.pin9
  N76: R13.Pin_0, J23.pin10
  N77: R14.Pin_0, J23.pin2
  N78: R15.Pin_0, J23.pin8
  N79: J23.pin7, R16.Pin_0

notes:
  HLQSTCEC
  (4067)
  A
  B
  C
  D
  (595)
  KILO-MUX
  ISP HEADER
