# Fritzing sketch id2175_Kiss_TNC_0 (saved by Fritzing 0.9.2b)
circuit board: 8.46667cm x 5.64444cm
breadboards: 1

parts:
  Arduino_Nano = Arduino Nano (Rev3.0)
  Jack_Breakout = TRRS 3.5mm Jack Breakout
  Q1 = NPN-Transistor [package="TO92 [THT]"]
  R1 = Resistor [tolerance=±5% resistance=1.5k package=THT]
  C1 = Ceramic Capacitor [capacitance=100nF package="100 mil [THT, multilayer]"]
  R2 = Resistor [tolerance=±5% resistance=100k package=THT]
  R3 = Resistor [tolerance=±5% resistance=10 package=THT]
  C2 = Ceramic Capacitor [capacitance=10nF package="100 mil [THT, multilayer]"]
  R4 = Resistor [tolerance=±5% resistance=10 package=THT]
  R5 = Resistor [tolerance=±5% resistance=10 package=THT]

nets:
  N1: Arduino_Nano.GND, Jack_Breakout.SLEEVE, Q1.C, R3.Pin_0, R5.Pin_0
  N2: Arduino_Nano.D6, R2.Pin_0, R3.Pin_1
  N3: Arduino_Nano.D10, R1.Pin_0
  N4: Arduino_Nano.A5, R4.Pin_0
  N5: Arduino_Nano.A0, C2.0, R4.Pin_1, R5.Pin_1
  N6: Jack_Breakout.RING2, C1.1
  N7: Jack_Breakout.RING1, Q1.E
  N8: Jack_Breakout.TIP, C2.1
  N9: Q1.B, R1.Pin_1
  N10: C1.0, R2.Pin_1

notes:
  KiSS TNC
  V 1.0
  Bob Wardecker
