# Fritzing sketch id2176_LichtKueche_0 (saved by Fritzing 0.9.2b)
circuit board: 8.46667cm x 5.64444cm
breadboards: 1

parts:
  Led1_Red = MOSFET-NCHANNEL [part_number="Mosfet Rot LED1" package=to220v]
  Led1_Green = MOSFET-NCHANNEL [part_number="Mosfet Grün LED1" package=to220v]
  Led1_Blue = MOSFET-NCHANNEL [part_number="Mosfet Blau LED1" package=to220v]
  Led2_Reed = MOSFET-NCHANNEL [part_number="Mosfet Ror LED2" package=to220v]
  Led2_Blue = MOSFET-NCHANNEL [part_number="Mosfet Blau LED2" package=to220v]
  R2 = Resistor [tolerance=±5% resistance=330 part_number="WiderStand Grün LED1" package=THT]
  R3 = Resistor [tolerance=±5% resistance=330 part_number="Widerstand Blau LED1" package=THT]
  R4 = Resistor [tolerance=±5% resistance=330 part_number="Widerstand Rot LED2" package=THT]
  R5 = Resistor [tolerance=±5% resistance=330 part_number="Widerstand Grün LED2" package=THT]
  R6 = Resistor [tolerance=±5% resistance=330 part_number="Widerstand Blau LED2" package=THT]
  LED1 = RGB LED (com. cathode, rgb) [package="5 mm [THT]"]
  LED2 = RGB LED (com. cathode, rgb) [package="5 mm [THT]"]
  Bauteil1 = Arduino Uno (Rev3)
  VCC1 = Battery block 9V [part_number="24Volt AC"]
  R1 = Resistor [tolerance=±5% resistance=330 part_number="Widerstand Rot LED1" package=THT]
  V1 = AC Power [voltage=5 frequency=60]  # not connected
  Led2_Green = MOSFET-NCHANNEL [part_number="Mosfet Grün LED2" package=to220v]
  VCC2 = Battery block 9V [part_number="24Volt AC"]

nets:
  N1: Led1_Red.G, R1.Pin_0
  N2: Led1_Red.D, LED1.red_anode
  N3: Led1_Red.S, Led1_Green.S, Led1_Blue.S, Led2_Reed.S, Led2_Blue.S, VCC1.-, Led2_Green.S, VCC2.-
  N4: Led1_Green.G, R2.Pin_0
  N5: Led1_Green.D, LED1.green_anode
  N6: Led1_Blue.G, R3.Pin_0
  N7: Led1_Blue.D, LED1.blue_anode
  N8: Led2_Reed.G, R4.Pin_0
  N9: Led2_Reed.D, LED2.red_anode
  N10: Led2_Blue.G, R6.Pin_0
  N11: Led2_Blue.D, LED2.blue_anode
  N12: R2.Pin_1, Bauteil1.D10_PWM/SS
  N13: R3.Pin_1, Bauteil1.D9_PWM
  N14: R5.Pin_0, Led2_Green.G
  N15: R5.Pin_1, Bauteil1.D5_PWM
  N16: R6.Pin_1, Bauteil1.D3_PWM
  N17: LED1.common_cathode, VCC1.+
  N18: LED2.common_cathode, VCC2.+
  N19: LED2.green_anode, Led2_Green.D
  N20: Bauteil1.D11_PWM/MOSI, R1.Pin_1
