# Fritzing sketch id2178_MBED_MQTT_0 (saved by Fritzing 0.7.4b)
breadboards: 1

parts:
  MBED1 = mbed
  LCD1 = LCD screen
  R1 = Rotary Potentiometer (Small) [maximum_resistance=100kΩ]

nets:
  GND: MBED1.GND, LCD1.VSS, LCD1.R/W, LCD1.LED-, R1.leg2
  N1: MBED1.pin15, LCD1.RS
  N2: MBED1.pin16, LCD1.E
  N3: MBED1.pin17, LCD1.DB4
  N4: MBED1.pin18, LCD1.DB5
  N5: MBED1.pin19, LCD1.DB6
  N6: MBED1.pin20, LCD1.DB7
  N7: MBED1.VOUT, LCD1.VDD, LCD1.LED+, R1.leg1
  N8: LCD1.V0, R1.wiper

notes:
  MAGJack goes here |
