# Fritzing sketch id2179_Untitled_Sketch_0 (saved by Fritzing 0.9.3b)

parts:
  Часть1 = Arduino Nano (Rev3.0)
  Часть2 = Bluetooth HC-05 Macho

nets:
  N1: Часть1.D10, Часть2.TXD
  N2: Часть1.D11/MOSI, Часть2.RXD
