# Fritzing sketch id217_Untitled_Sketch_0 (saved by Fritzing 0.9.3b)
breadboards: 1

parts:
  Part1 = Arduino Uno (Rev3)
  Q1 = NPN-Transistor [package="TO92 [THT]"]
  C1 = Ceramic Capacitor [capacitance=100nF package="100 mil [THT, multilayer]"]
  LCD1 = LCD screen
  R1 = Resistor [tolerance=±5% resistance=221 package=THT]
  R2 = Resistor [tolerance=±5% resistance=220 package=THT]
  R3 = Resistor [tolerance=±5% resistance=1k package=THT]
  LED1 = LED - 5mm [color="Red (633nm)" package="5 mm [THT]"]
  U1 = DIODE-ZENER [package=sod-323]
  U2 = TMP36 [package=to-92-kit]
  K1 = Relay [part_number=FRS1B-S package=THT]

nets:
  N1: Part1.A0, U2.VOUT
  N2: Part1.D8, R3.Pin_0
  N3: Part1.D9_PWM, LED1.anode
  GND: Part1.GND, Q1.E, C1.1, LCD1.VSS, LCD1.V0, LCD1.R/W, R1.Pin_1, R2.Pin_1, U2.GND
  N4: Part1.D2, LCD1.RS
  N5: Part1.D3_PWM, LCD1.E
  N6: Part1.D4, LCD1.DB4
  N7: Part1.D5_PWM, LCD1.DB5
  N8: Part1.D6_PWM, LCD1.DB6
  N9: Part1.D7, LCD1.DB7
  5V: Part1.5V, C1.0, LCD1.VDD, LCD1.LED+, U1.C, U2.VCC, K1.C1, K1.C2, K1.COIL2
  N10: Q1.B, R3.Pin_1
  N11: Q1.C, U1.A, K1.COIL1
  N12: LCD1.LED-, R1.Pin_0
  N13: R2.Pin_0, LED1.cathode, K1.B
