# Fritzing sketch id2180_Temp_LCD_0 (saved by Fritzing 0.9.2b)

parts:
  RHT1 = Humidity and Temperature Sensor RHT03
  R1 = Resistor [tolerance=±5% resistance=220 package=THT]
  Bauteil1 = Arduino Leonardo (Rev3b)
  LCD1 = LCD screen  # not connected
  IIC1 = iic_converter

nets:
  VCC: RHT1.Vcc, R1.Pin_1, Bauteil1.3V3
  N1: RHT1.GND_1, Bauteil1.D7
  N2: RHT1.GND_2, Bauteil1.GND, IIC1.connector16
  N3: Bauteil1.5V, IIC1.connector17
  N4: Bauteil1.SDA, IIC1.connector18
  N5: Bauteil1.SCL, IIC1.connector19
  N6: IIC1.connector20, IIC1.connector21

notes:
  I²C Modul für das Display
