# Fritzing sketch id2182_Untitled_Sketch_0 (saved by Fritzing 0.9.3b)
breadboards: 2

parts:
  Bauteil1 = Arduino Uno (Rev3)
  LED1 = LED - 5mm [color="Blue (525nm)" package="5 mm [THT]"]
  LED2 = LED - 5mm [color="Green (570nm)" package="5 mm [THT]"]
  LED3 = LED - 5mm [color="Red (633nm)" package="5 mm [THT]"]
  R1 = Resistor [tolerance=±5% resistance=220 package=THT]
  T1 = LM35 Temperature Sensor [package="TO92 [THT]"]
  R2 = Trimmer Potentiometer [maximum_resistance=10kΩ package=THT]
  IC1 = H-Bridge [package=THT]
  J1 = Piezo Speaker
  M1 = DC Motor
  VCC1 = Battery block 9V

nets:
  N1: Bauteil1.A0, T1.Vout
  N2: Bauteil1.A1, R2.wiper
  N3: Bauteil1.D11_PWM/MOSI, LED3.anode
  N4: Bauteil1.D12/MISO, LED2.anode
  N5: Bauteil1.D13/SCK, LED1.anode
  GND: Bauteil1.GND, R1.Pin_1, T1.GND, R2.leg1, IC1.GND1, IC1.GND2, J1.pin1, VCC1.-
  N6: Bauteil1.D2, IC1.2A
  N7: Bauteil1.D5_PWM, IC1.1A
  N8: Bauteil1.D6_PWM, IC1.1_2EN
  N9: Bauteil1.D7, J1.pin2
  N10: Bauteil1.5V, T1.+Vs, R2.leg2, IC1.VCC1
  N11: LED2.cathode, LED3.cathode, R1.Pin_0
  N12: IC1.1Y, M1.pin_1
  N13: IC1.2Y, M1.pin_2
  N14: IC1.VCC2, VCC1.+
