# Fritzing sketch id2183_KneeActivityMonitor_0 (saved by Fritzing 0.9.3b)
breadboards: 1

parts:
  Part1 = Arduino Uno (Rev3)
  R1 = Basic Flex Resistor
  R2 = Resistor [tolerance=±5% resistance=220 package=THT]
  Part4 = Bluetooth HC-05 Macho
  GY1 = GY-521 (MPU-6050) [form="♀ (female)"]
  J1 = Piezo Speaker

nets:
  N1: Part1.A0, R1.Pin_2, R2.Pin_1
  N2: Part1.A4/SDA, GY1.connector3
  N3: Part1.A5/SCL, GY1.connector2
  N4: Part1.D9_PWM, J1.pin2
  GND: Part1.GND, R1.pin_1, Part4.GND, GY1.connector1, J1.pin1
  N5: Part1.D0/RX, Part4.TXD
  N6: Part1.D1/TX, Part4.RXD
  N7: Part1.D2, GY1.connector7
  5V: Part1.5V, Part4.VCC, GY1.connector0
