# Fritzing sketch id2184_Leds_auto_increible_0 (saved by Fritzing 0.9.2b)
breadboards: 1

parts:
  R1 = Resistor [tolerance=±5% resistance=220 package=THT]
  R2 = Resistor [tolerance=±5% resistance=220 package=THT]
  R3 = Resistor [tolerance=±5% resistance=220 package=THT]
  R4 = Resistor [tolerance=±5% resistance=220 package=THT]
  R5 = Resistor [tolerance=±5% resistance=220 package=THT]
  R6 = Resistor [tolerance=±5% resistance=220 package=THT]
  R7 = Resistor [tolerance=±5% resistance=220 package=THT]
  R8 = Resistor [tolerance=±5% resistance=220 package=THT]
  LED1 = LED - 5mm [color="Red (633nm)" current=1 package="5 mm [THT]"]
  LED2 = LED - 5mm [color="Red (633nm)" package="5 mm [THT]"]
  LED3 = LED - 5mm [color="Red (633nm)" package="5 mm [THT]"]
  LED4 = LED - 5mm [color="Red (633nm)" package="5 mm [THT]"]
  LED5 = LED - 5mm [color="Red (633nm)" package="5 mm [THT]"]
  LED6 = LED - 5mm [color="Red (633nm)" package="5 mm [THT]"]
  LED7 = LED - 5mm [color="Red (633nm)" package="5 mm [THT]"]
  LED8 = LED - 5mm [color="Red (633nm)" package="5 mm [THT]"]
  Parte1 = Arduino Uno (Rev3)

nets:
  N1: R1.Pin_0, R2.Pin_0, R3.Pin_0, R4.Pin_0, R5.Pin_0, R6.Pin_0, R7.Pin_0, R8.Pin_0
  N2: R1.Pin_1, LED8.cathode
  N3: R2.Pin_1, LED1.cathode
  N4: R3.Pin_1, LED2.cathode
  N5: R4.Pin_1, LED3.cathode
  N6: R5.Pin_1, LED4.cathode
  N7: R6.Pin_1, LED5.cathode
  N8: R7.Pin_1, LED6.cathode
  N9: R8.Pin_1, LED7.cathode
  N10: LED1.anode, Parte1.D2
  N11: LED2.anode, Parte1.D3_PWM
  N12: LED3.anode, Parte1.D4
  N13: LED4.anode, Parte1.D5_PWM
  N14: LED5.anode, Parte1.D6_PWM
  N15: LED6.anode, Parte1.D7
  N16: LED7.anode, Parte1.D8
  N17: LED8.anode, Parte1.D9_PWM
