# Fritzing sketch id2185_code_lock_0 (saved by Fritzing 0.9.2b)
circuit board: 8.46667cm x 5.64444cm
breadboards: 1

parts:
  IC1 = PIC16F690
  J1 = PICICSP [form="♂ (male)"]
  J2 = LCD10contact [form="♂ (male)"]
  S1 = Pushbutton [package="[THT]"]
  U1 = POT [package=trim_pot]
  R1 = Trimmer Potentiometer [maximum_resistance=10kΩ package=THT]
  R2 = Resistor [tolerance=±10% resistance=12k package=THT]
  R3 = Resistor [tolerance=±10% resistance=10k package=THT]

nets:
  N1: IC1.connector0, J1.connector1, U1.A, R1.leg2, R2.Pin_0, R3.Pin_1
  N2: IC1.connector3, J1.connector0, R3.Pin_0
  N3: IC1.connector6, J2.connector13
  N4: IC1.connector10, J2.connector5
  N5: IC1.connector11, S1.Pin_3, S1.Pin_4, R2.Pin_1
  N6: IC1.connector12, J2.connector3
  N7: IC1.connector13, J2.connector12
  N8: IC1.connector14, J2.connector11
  N9: IC1.connector15, J2.connector10
  N10: IC1.connector16, R1.wiper
  N11: IC1.connector17, J1.connector4
  N12: IC1.connector18, J1.connector3
  N13: IC1.connector19, J1.connector2, S1.Pin_1, S1.Pin_2, U1.S, R1.leg1
  N14: J2.connector2, U1.E
