# Fritzing sketch id2199_mbed_lpc1114_i2c_konashi_0 (saved by Fritzing 0.9.3b)
breadboards: 1

parts:
  IC1 = LPC1114_DIL
  S1 = Pushbutton [package="[THT]"]
  LED1 = smd LED [color="Red (633nm)" package="1206 [SMD]"]
  R2 = Resistor [tolerance=±5% resistance=330 package=THT]
  R3 = Resistor [tolerance=±5% resistance=2.2k package=THT]
  R4 = Resistor [tolerance=±5% resistance=2.2k package=THT]
  konashi = mystery part, 8 pins [chip_label=?]

nets:
  N1: IC1.connector5, R3.Pin_1, konashi.pin4
  N2: IC1.connector13, S1.Pin_3, S1.Pin_4
  N3: IC1.connector14, R2.Pin_0
  N4: IC1.connector27, R4.Pin_1, konashi.pin3
  N5: S1.Pin_1, S1.Pin_2, LED1.anode, konashi.pin8
  N6: LED1.cathode, R2.Pin_1
  N7: R3.Pin_0, R4.Pin_0, konashi.pin2
