# Fritzing sketch id219_AABTank_0 (saved by Fritzing 0.8.3b)

parts:
  J1 = female pin header, 8 pins [form="♀ (female)"]
  J2 = female pin header, 8 pins [form="♀ (female)"]
  J3 = female pin header, 4 pins [form="♀ (female)"]  # not connected
  J4 = female pin header, 2 pins [form="♀ (female)"]  # not connected
  J5 = female pin header, 2 pins [form="♀ (female)"]
  J6 = female pin header, 2 pins [form="♀ (female)"]
  J7 = female pin header, 2 pins [form="♀ (female)"]
  J8 = female pin header, 2 pins [form="♀ (female)"]
  J9 = female pin header, 2 pins [form="♀ (female)"]
  JP1 = Header 3 [package=molex-1x3_lock]  # not connected
  JP2 = Header 3 [package=molex-1x3_lock]  # not connected
  JP3 = Header 2 [package=screwterminal-3.5mm-2_lock]  # not connected
  JP4 = Header 2 [package=screwterminal-3.5mm-2_lock]  # not connected
  JP5 = Header 2 [package=screwterminal-3.5mm-2_lock]  # not connected
  JP6 = Header 2 [package=screwterminal-3.5mm-2_lock]  # not connected
  JP7 = Header 2 [package=screwterminal-3.5mm-2_lock]  # not connected
  U1 = 74HC595 [package="DIP16 [THT]"]  # not connected
  IC1 = L293D [package=THT]  # not connected
  IC2 = L293D [package=THT]  # not connected
  JP8 = Jumper [package=sj_2s-no-ns]  # not connected
  C1 = Electrolytic Capacitor [capacitance=1µF package="100 mil [THT, electrolytic]"]  # not connected
  C2 = Electrolytic Capacitor [capacitance=1µF package="100 mil [THT, electrolytic]"]  # not connected
  C3 = Electrolytic Capacitor [capacitance=1µF package="100 mil [THT, electrolytic]"]  # not connected
  C4 = Electrolytic Capacitor [capacitance=1µF package="100 mil [THT, electrolytic]"]  # not connected
  C5 = Tantalum Capacitor [capacitance="1 μF" package="100 mil [THT, tantalum]"]  # not connected
  C6 = Tantalum Capacitor [capacitance="1 μF" package="100 mil [THT, tantalum]"]  # not connected
  C7 = Tantalum Capacitor [capacitance="1 μF" package="100 mil [THT, tantalum]"]  # not connected
  R1 = Resistor [tolerance=±5% resistance=220 package=THT]  # not connected
  R2 = Resistor [tolerance=±5% resistance=220 package=THT]  # not connected
  LED1 = LED - 5mm [color="Red (633nm)" package="5 mm [THT]"]  # not connected
  S1 = Pushbutton [package="[THT]"]  # not connected
  R3 = RPACK* [package=rpack-sip-pth-5]  # not connected
  R4 = RPACK* [package=rpack-sip-pth-5]  # not connected
  Part1 = Arduino Uno (Rev3)
  Part2 = Bluetooth Mate Silver
  VCC1 = Battery block 9V  # not connected
  M1 = DC Motor  # not connected
  M2 = DC Motor  # not connected

nets:
  N1: J1.pin1, Part1.D7
  N2: J1.pin2, Part1.D6_PWM
  N3: J1.pin3, Part1.D5_PWM
  N4: J1.pin4, Part1.D4
  N5: J1.pin5, Part1.D3_PWM
  N6: J1.pin6, Part1.D2
  N7: J2.pin1, Part1.AREF
  N8: J2.pin2, J6.pin2, J7.pin2, Part1.GND
  N9: J2.pin3, Part1.ICSP_SCK, Part1.D13/SCK
  N10: J2.pin4, Part1.ICSP_MISO, Part1.D12/MISO
  N11: J2.pin5, Part1.ICSP_MOSI, Part1.D11_PWM/MOSI
  N12: J2.pin6, Part1.D10_PWM/SS
  N13: J2.pin7, Part1.D9_PWM
  N14: J2.pin8, Part1.D8
  N15: J5.pin2, Part1.VIN
  N16: J7.pin1, Part2.VCC
  N17: J8.pin1, Part2.CTS_5V
  N18: J8.pin2, Part1.5V
  N19: J9.pin1, Part1.RESET
  N20: J9.pin2, Part1.3V3
  N21: Part1.D0/RX, Part2.TX_5V
  N22: Part1.D1/TX, Part2.RX_5V

notes:
  XXXXXX
  JY-MCU
  V1.05
  5 VCC
  ADAFRUIT MOTOR SHIELD
  RXD
  TXD
  GND
  VCC
