# Fritzing sketch id21_2.L293D+2DCmoto_0 (saved by Fritzing 0.9.3b)
breadboards: 1

parts:
  元件1 = Arduino Uno (Rev3)
  IC1 = L293D [package=THT]
  M1 = DC Motor
  M2 = DC Motor
  VCC1 = Battery block 9V

nets:
  N1: 元件1.A0, IC1.In_3
  N2: 元件1.A1, IC1.In_4
  N3: 元件1.GND, IC1.0V, VCC1.-
  N4: 元件1.D4, IC1.In_1
  N5: 元件1.D5_PWM, IC1.In_2
  N6: 元件1.5V, IC1.+V
  N7: IC1.Out_1_(_Controlled_by_Enable_1_), M2.pin_1
  N8: IC1.Out_2_(_Controlled_by_Enable_1_), M2.pin_2
  N9: IC1.+Vmotor, VCC1.+
  N10: IC1.Out_3_(_Controlled_by_Enable_2_), M1.pin_2
  N11: IC1.Out_4_(_Controlled_by_Enable_2_), M1.pin_1

notes:
  Arduino UNO
  DC Motor
  9V Battery
