# Fritzing sketch id2200_Untitled_Sketch_0 (saved by Fritzing 0.8.3b)
circuit board: 12.6497cm x 6.56067cm

parts:
  R2 = Resistor [tolerance=±5% resistance=220 package=THT]
  R3 = Resistor [tolerance=±5% resistance=220 package=THT]
  R5 = Resistor [tolerance=±5% resistance=220 package=THT]
  R6 = Resistor [tolerance=±5% resistance=220 package=THT]
  R7 = Resistor [tolerance=±5% resistance=220 package=THT]
  R8 = Resistor [tolerance=±5% resistance=220 package=THT]
  S2 = Pushbutton [package=THT]
  S3 = Pushbutton [package=THT]
  S7 = Pushbutton [package=THT]
  S9 = Pushbutton [package=THT]
  R9 = Trimmer Potentiometer [maximum_resistance=10kΩ package=THT]
  R10 = Trimmer Potentiometer [maximum_resistance=10kΩ package=THT]
  R12 = Trimmer Potentiometer [maximum_resistance=10kΩ package=THT]
  R14 = Trimmer Potentiometer [maximum_resistance=10kΩ package=THT]
  R15 = Trimmer Potentiometer [maximum_resistance=10kΩ package=THT]
  R16 = Trimmer Potentiometer [maximum_resistance=10kΩ package=THT]
  Q3 = NPN-Transistor [package="TO92 [THT]"]
  R17 = Resistor [tolerance=±5% resistance=220 package=THT]
  R19 = Resistor [tolerance=±5% resistance=220 package=THT]
  R20 = Resistor [tolerance=±5% resistance=220 package=THT]
  C1 = Electrolytic Capacitor [capacitance=1µF package="100 mil [THT, electrolytic]"]
  C2 = Electrolytic Capacitor [capacitance=1µF package="100 mil [THT, electrolytic]"]
  VCC1 = Battery block 9V
  SPKR1 = Loudspeaker  # not connected
  R21 = Resistor [tolerance=±5% resistance=220 package=THT]
  R22 = Trimmer Potentiometer [maximum_resistance=10kΩ package=THT]
  R23 = Resistor [tolerance=±5% resistance=220 package=THT]
  R24 = Trimmer Potentiometer [maximum_resistance=10kΩ package=THT]
  R26 = Resistor [tolerance=±5% resistance=220 package=THT]
  S12 = Pushbutton [package=THT]
  S13 = Pushbutton [package=THT]
  S14 = Pushbutton [package=THT]
  Q6 = NPN-Transistor [package="TO92 [THT]"]
  Q7 = NPN-Transistor [package="TO92 [THT]"]
  S15 = Pushbutton [package=THT]

nets (from the pcb view):
  N1: R2.Pin_0, R12.wiper
  N2: R2.Pin_1, S13.leg0
  N3: R3.Pin_0, R14.wiper
  N4: R3.Pin_1, S3.leg0
  N5: R5.Pin_0, R16.wiper
  N6: R5.Pin_1, S9.leg0
  N7: R6.Pin_0, C2.+, Q7.B
  N8: R6.Pin_1, S2.leg1, S3.leg1, S7.leg1, S9.leg1, R17.Pin_1, R20.Pin_1, R21.Pin_1, R26.Pin_1, S12.leg1, S13.leg1, S14.leg1, S15.leg0, S15.leg1
  N9: R7.Pin_0, R10.wiper
  N10: R7.Pin_1, S7.leg0
  N11: R8.Pin_0, R9.wiper
  N12: R8.Pin_1, S2.leg0
  N13: R9.leg1, R9.leg2, R10.leg1, R10.leg2, R12.leg1, R12.leg2, R14.leg1, R14.leg2, R15.leg1, R15.leg2, R16.leg1, R16.leg2, Q3.B, R22.leg1, R22.leg2, R24.leg1, R24.leg2
  N14: R15.wiper, R23.Pin_0
  N15: Q3.C, C2.-
  N16: R17.Pin_0, R22.wiper
  N17: R19.Pin_0, R24.wiper
  N18: R19.Pin_1, S12.leg0
  N19: C1.+, R26.Pin_0, Q6.B, Q7.E
  N20: VCC1.+, Q6.C, Q7.C
  N21: R23.Pin_1, S14.leg0

notes:
  krach bumsdings
