# Fritzing sketch id2203_kuliah_0 (saved by Fritzing 0.9.3b)

parts:
  RHT1 = Humidity and Temperature Sensor RHT03
  VCC1 = Battery block 9V
  J1 = Basic Servo
  Part1 = Arduino Leonardo (Rev3b)

nets:
  VCC: RHT1.Vcc, J1.vcc, Part1.5V
  N1: RHT1.Data-signal, Part1.D3_PWM/SCL
  GND: RHT1.GND_2, VCC1.-, J1.gnd, Part1.GND
  N2: VCC1.+, Part1.VIN
  N3: J1.pulse, Part1.D8/A8
