# Fritzing sketch id2206_stepper_cd_serpentine_0 (saved by Fritzing 0.7.4b)
breadboards: 1

parts:
  Arduino1 = Arduino
  M1 = Stepper Motor - Bipolar
  Power_plug1 = Power plug  # not connected
  L293 = L293D [package=THT]

nets:
  N1: Arduino1.GND, L293.0V
  N2: Arduino1.D11, L293.In_4
  N3: Arduino1.D10, L293.In_3
  N4: Arduino1.D9, L293.In_2
  N5: Arduino1.D8, L293.In_1
  N6: Arduino1.+5V, L293.Enable_1, L293.+Vmotor, L293.Enable_2, L293.+V
  N7: M1.A, L293.Out_4_(_Controlled_by_Enable_2_)
  N8: M1.C, L293.Out_3_(_Controlled_by_Enable_2_)
  N9: M1.B, L293.Out_2_(_Controlled_by_Enable_1_)
  N10: M1.D, L293.Out_1_(_Controlled_by_Enable_1_)

notes:
  The motor used in this example is a salvaged cd-rom stepper. You can identify it because it is attached to a "serpentine". The schematic is based on this very simple yet functional one.
  http://blog.whattomake.co.kr/158
  It works very well with the examples library of Arduino environment.
  You can use the +5v from arduino board or an external supply if you need more voltage.
