# Fritzing sketch id2207_19_L293_DC_Motor_Control_Fritzing_0 (saved by Fritzing 0.8.7b)
breadboards: 1

parts:
  Part1 = Arduino Uno (Rev3)
  M1 = DC Motor
  R1 = Rotary Potentiometer (Small) [maximum_resistance=100kΩ package=THT]
  IC1 = L293D [package=THT]

nets:
  N1: Part1.A0, R1.wiper
  N2: Part1.D9_PWM, IC1.In_1
  N3: Part1.D10_PWM/SS, IC1.In_2
  N4: Part1.5V, R1.leg1, IC1.+V
  N5: Part1.GND, R1.leg2, IC1.0V
  N6: M1.pin_1, IC1.Out_1_(_Controlled_by_Enable_1_)
  N7: M1.pin_2, IC1.Out_2_(_Controlled_by_Enable_1_)
