# Fritzing sketch id2209_L293D_0 (saved by Fritzing 0.9.1b)
breadboards: 1

parts:
  L293D = L293D [package=THT]
  VCC = 4 x AAA Battery Mount [part_number=6V]
  R1 = Resistor [tolerance=±5% resistance=1k package=THT]
  R2 = Resistor [tolerance=±5% resistance=1k package=THT]
  S1 = Pushbutton [package="[THT]"]
  S2 = Pushbutton [package="[THT]"]
  DC_Motor = DC Motor

nets:
  N1: L293D.Enable_1, L293D.+Vmotor, L293D.Enable_2, L293D.+V, VCC.+, R1.Pin_1, R2.Pin_1
  N2: L293D.In_1, R1.Pin_0, S2.Pin_3, S2.Pin_4
  N3: L293D.Out_1_(_Controlled_by_Enable_1_), DC_Motor.pin_1
  N4: L293D.0V, VCC.-, S1.Pin_1, S1.Pin_2, S2.Pin_1, S2.Pin_2
  N5: L293D.Out_2_(_Controlled_by_Enable_1_), DC_Motor.pin_2
  N6: L293D.In_2, R2.Pin_0, S1.Pin_3, S1.Pin_4
