# Fritzing sketch id220_HC_06_0 (saved by Fritzing 0.9.3b)
breadboards: 1

parts:
  PIC_16F877A1 = PICAXE-40X [part_number=PIC16F887 package=THT]
  Onderdeel1 = HC-06

nets:
  N1: PIC_16F877A1.+V, Onderdeel1.connector15
  N2: PIC_16F877A1.0V, Onderdeel1.connector14
  N3: PIC_16F877A1.In/Out_C6, Onderdeel1.connector12
  N4: PIC_16F877A1.In/Out_C7, Onderdeel1.connector13
