# Fritzing sketch id2211_L293D_0 (saved by Fritzing 0.9.2b)

parts:
  IC1 = L293D [package=THT]
  M1 = DC Motor
  M2 = DC Motor

nets:
  N1: IC1.Out_1_(_Controlled_by_Enable_1_), M2.pin_2
  N2: IC1.Out_2_(_Controlled_by_Enable_1_), M2.pin_1
  N3: IC1.Out_3_(_Controlled_by_Enable_2_), M1.pin_2
  N4: IC1.Out_4_(_Controlled_by_Enable_2_), M1.pin_1

notes:
  Enable pin 1
  Input pin 1
  Output pin 1
  Ground
  Output pin 2
  Input pin 2
  VDD for motor
  VDD for IC
  Input pin 4
  Output pin 4
  Output pin 3
  Input pin 3
  Inable pin 2
  Use Enable 1 & 2 to control speed of motors.
  Ground must be connected to MCU's ground.
