# Fritzing sketch id2212_unol293d2steper_0 (saved by Fritzing 0.8.7b)
breadboards: 1

parts:
  Часть1 = Arduino Uno (Rev3)
  IC1 = L293D [package=THT]
  IC2 = L293D [package=THT]
  M1 = Stepper Motor - Bipolar
  M2 = Stepper Motor - Bipolar

nets:
  N1: Часть1.D8, IC2.In_1
  N2: Часть1.D9_PWM, IC2.In_3
  N3: Часть1.D10_PWM/SS, IC2.In_2
  N4: Часть1.D11_PWM/MOSI, IC2.In_4
  N5: Часть1.GND, IC1.0V, IC2.0V
  N6: Часть1.D5_PWM, IC1.In_3
  N7: Часть1.D7, IC1.In_4
  N8: Часть1.5V, IC1.Enable_2, IC1.+V, IC2.Enable_1, IC2.+Vmotor, IC2.Enable_2, IC2.+V
  N9: IC1.Out_3_(_Controlled_by_Enable_2_), M2.B
  N10: IC1.Out_4_(_Controlled_by_Enable_2_), M2.D
  N11: IC2.Out_1_(_Controlled_by_Enable_1_), M1.A
  N12: IC2.Out_2_(_Controlled_by_Enable_1_), M1.C
  N13: IC2.Out_3_(_Controlled_by_Enable_2_), M1.B
  N14: IC2.Out_4_(_Controlled_by_Enable_2_), M1.D
