# Fritzing sketch id2216_Week_20_H_Bridge_Lab_0 (saved by Fritzing 0.9.2b)
breadboards: 1

parts:
  Part1 = Arduino Nano (Rev3.0) (ICSP)
  Q1 = PNP-Transistor [package="TO92 [THT]"]
  Q2 = PNP-Transistor [package="TO92 [THT]"]
  R1 = Rotary Potentiometer (Small) [maximum_resistance=100kΩ package=THT]
  VCC1 = Battery
  S1 = Pushbutton [package="[THT]"]
  C1 = Electrolytic Capacitor [capacitance=1µF package="100 mil [THT, electrolytic]"]
  Q4 = Basic FET N-Channel [package="TO220 [THT]"]
  Q5 = Basic FET N-Channel [package="TO220 [THT]"]
  M1 = DC Motor
  R2 = Resistor [tolerance=±5% resistance=1k package=THT]
  R3 = Resistor [tolerance=±5% resistance=1k package=THT]
  R4 = Resistor [tolerance=±5% resistance=6.8 package=THT]
  R5 = Resistor [tolerance=±5% resistance=6.8 package=THT]
  D1 = Rectifier Diode [part_number=1N4001 package="300 mil [THT]"]
  D2 = Rectifier Diode [part_number=1N4001 package="300 mil [THT]"]
  D3 = Rectifier Diode [part_number=1N4001 package="300 mil [THT]"]
  D4 = Rectifier Diode [part_number=1N4001 package="300 mil [THT]"]

nets:
  N1: Part1.GND, R1.leg2, VCC1.-, S1.Pin_3, S1.Pin_4, C1.-, Q4.source, Q5.source, D1.anode, D2.anode
  N2: Part1.D3, R3.Pin_0
  N3: Part1.D5, R5.Pin_0
  N4: Part1.D6, R2.Pin_0
  N5: Part1.D11/MOSI, R4.Pin_1
  N6: Part1.5V, Q1.E, Q2.E, R1.leg1, VCC1.+, C1.+, D3.cathode, D4.cathode
  N7: Part1.A7, R1.wiper
  N8: Part1.D13/SCK, S1.Pin_1, S1.Pin_2
  N9: Q1.B, R2.Pin_1
  N10: Q1.C, Q4.drain, M1.pin_1, D1.cathode, D3.anode
  N11: Q2.B, R3.Pin_1
  N12: Q2.C, Q5.drain, M1.pin_2, D2.cathode, D4.anode
  N13: Q4.gate, R5.Pin_1
  N14: Q5.gate, R4.Pin_0
