# Fritzing sketch id2219_lab_uino_l298_0 (saved by Fritzing 0.8.3b)
perfboards: 1

parts:
  M1 = DC Motor
  U1 = L298 [package=multiwatt15]
  VCC1 = Battery block 9V
  J1 = female pin header, 5 pins [form="♀ (female)"]  # not connected
  J2 = female pin header, 5 pins [form="♀ (female)"]  # not connected
  J3 = female pin header, 5 pins [form="♀ (female)"]
  J4 = female pin header, 5 pins [form="♀ (female)"]
  J5 = female pin header, 10 pins [form="♀ (female)"]  # not connected
  J6 = female pin header, 6 pins [form="♀ (female)"]  # not connected
  J7 = female pin header, 3 pins [form="♀ (female)"]  # not connected
  J8 = female pin header, 3 pins [form="♀ (female)"]  # not connected
  J9 = female pin header, 3 pins [form="♀ (female)"]  # not connected
  J10 = female pin header, 3 pins [form="♀ (female)"]  # not connected
  J11 = female pin header, 3 pins [form="♀ (female)"]  # not connected
  J12 = female pin header, 3 pins [form="♀ (female)"]  # not connected
  M2 = DC Motor

nets:
  N1: M1.pin_1, U1.OUT2
  N2: M1.pin_2, U1.OUT1
  N3: U1.CSA, U1.GND, U1.CSB, VCC1.-, J3.pin1
  N4: U1.VS, J4.pin1
  N5: U1.IN1, J3.pin4
  N6: U1.ENA, J4.pin3
  N7: U1.IN2, J4.pin4
  N8: U1.VLS, VCC1.+
  N9: U1.IN3, J4.pin5
  N10: U1.ENB, J3.pin3
  N11: U1.IN4, J3.pin5
  N12: U1.OUT3, M2.pin_2
  N13: U1.OUT4, M2.pin_1

notes:
  Conectores placa
  Lab_Uino
  Ponte H
  L298
