# Fritzing sketch id221_abotingObstacleRobot_0 (saved by Fritzing 0.9.2b)
breadboards: 1

parts:
  パーツ1 = Arduino Motor Shield (Rev3)
  パーツ2 = Arduino Uno (Rev3)  # not connected
  J1 = Infrared Proximity Sensor
  C1 = Ceramic Capacitor [capacitance=100nF package="100 mil [THT, multilayer]"]
  LED1 = LED - 5mm [color="Green (555nm)" package="5 mm [THT]"]
  R1 = Resistor [tolerance=±5% resistance=220 package=THT]
  M1 = DC Motor
  M2 = DC Motor

nets:
  N1: パーツ1.A1, J1.Vout, C1.0, C1.1
  N2: パーツ1.D13/DirB, R1.Pin_0
  GND: パーツ1.GND, J1.GND, LED1.anode
  N3: パーツ1.B-, M1.pin_2
  N4: パーツ1.B+, M1.pin_1
  N5: パーツ1.A-, M2.pin_2
  N6: パーツ1.A+, M2.pin_1
  5V: パーツ1.5V, J1.Vcc
  N7: LED1.cathode, R1.Pin_1
