# Fritzing sketch id2220_Labo_functiegenerator_0 (saved by Fritzing 0.9.3b)
breadboards: 1

parts:
  S1 = Pushbutton [package="[THT]"]
  S2 = Pushbutton [package="[THT]"]
  S3 = Pushbutton [package="[THT]"]
  IC2 = 9477af554f7719aad1b4c8c093186053 [part_number=PCF8591]
  R1 = Resistor [tolerance=±5% resistance=330 package=THT]
  R2 = Resistor [tolerance=±5% resistance=330 package=THT]
  R3 = Resistor [tolerance=±5% resistance=330 package=THT]
  Onderdeel1 = Arduino Uno (Rev3) - ICSP
  U1 = POT [package=pot_alpha_rv16af-20]
  U2 = POT [package=pot_alpha_rv16af-20]
  R4 = Resistor [tolerance=±5% resistance=330 package=THT]
  R5 = Resistor [tolerance=±5% resistance=330 package=THT]

nets:
  N1: S1.Pin_1, S1.Pin_2, S2.Pin_1, S2.Pin_2, S3.Pin_1, S3.Pin_2, IC2.connector5, IC2.connector6, IC2.connector7, IC2.connector14, IC2.connector16, Onderdeel1.5V, U1.A, U1.E, U2.A, U2.E, R4.Pin_1, R5.Pin_1
  N2: S1.Pin_3, S1.Pin_4, R1.Pin_0, Onderdeel1.D2
  N3: S2.Pin_3, S2.Pin_4, R3.Pin_0, Onderdeel1.D3_PWM
  N4: S3.Pin_3, S3.Pin_4, R2.Pin_0, Onderdeel1.D4
  N5: IC2.connector8, IC2.connector12, R1.Pin_1, R2.Pin_1, R3.Pin_1, Onderdeel1.GND
  N6: IC2.connector9, Onderdeel1.A4/SDA, R4.Pin_0
  N7: IC2.connector10, Onderdeel1.A5/SCL, R5.Pin_0
  N8: Onderdeel1.A0, U2.S
  N9: Onderdeel1.A1, U1.S
