# Fritzing sketch id2220_hydraulicreverse02 (saved by Fritzing 0.6.3b)
breadboards: 1

parts:
  IC1 = IC, DIP package, 14 pins [chip_label=IC spacing=300mil]
  J1 = screw terminal, 4 pins
  Solenoids = screw terminal, 2 pins
  3_3V_reg = Voltage Regulator - 3.3V [package="TO220 [THT]"]
  R1 = Resistor [tolerance=±5% resistance=220 package=THT]
  J4 = Screw terminal - 2 pins [package=THT]
  J5 = Screw terminal - 2 pins [package=THT]
  R2 = Resistor [tolerance=±5% resistance=220 package=THT]
  R3 = Resistor [tolerance=±5% resistance=220 package=THT]
  R4 = Resistor [tolerance=±5% resistance=220 package=THT]
  R5 = Resistor [tolerance=±5% resistance=220 package=THT]
  R6 = Resistor [tolerance=±5% resistance=220 package=THT]
  C1 = Electrolytic Capacitor [capacitance=1µF package="100 mil [THT, electrolytic]"]
  part = Ceramic Capacitor [capacitance=100nF package="100 mil [THT, multilayer]"]
  REV_Relay = Componente_sem_nome
  FWD_Relay = Componente_sem_nome
  D1 = Rectifier Diode [part_number=1N4001 package="300 mil [THT]"]
  D2 = Rectifier Diode [part_number=1N4001 package="300 mil [THT]"]
  Q1 = NPN-Transistor [package="TO92 [THT]"]
  Q2 = NPN-Transistor [package="TO92 [THT]"]
  Reverse = LED - 5mm [color="Red (633nm)" package="5 mm [THT]"]
  Forward = LED - 5mm [color="Red (633nm)" package="5 mm [THT]"]
  Forward_2 = LED - 5mm [color="Red (633nm)" package="5 mm [THT]"]
  Reverse_2 = LED - 5mm [color="Red (633nm)" package="5 mm [THT]"]
  Pressure = LED - 5mm [color="Red (633nm)" package="5 mm [THT]"]
  R9 = Resistor [tolerance=±5% resistance=220 package=THT]
  R10 = Resistor [tolerance=±5% resistance=220 package=THT]
  R11 = Resistor [tolerance=±5% resistance=220 package=THT]
  R12 = Resistor [tolerance=±5% resistance=220 package=THT]
  R13 = Resistor [tolerance=±5% resistance=220 package=THT]
  Fuse = Reed switch [package=THT]

nets:
  N1: IC1.pin1, J1.pin4, 3_3V_reg.GND, R1.Pin_0, part.0, REV_Relay.connector1, FWD_Relay.connector1, D1.anode, D2.anode
  N2: IC1.pin5, J5.pin1, R4.Pin_1, R9.Pin_1
  N3: IC1.pin6, J4.pin2, R3.Pin_1, R10.Pin_1
  N4: IC1.pin7, J4.pin1, R2.Pin_1, R11.Pin_1
  N5: IC1.pin8, R5.Pin_0, Reverse.cathode, Reverse.anode, R13.Pin_1
  N6: IC1.pin9, R6.Pin_0, Forward.cathode, Forward.anode, R12.Pin_1
  N7: IC1.pin10, R1.Pin_1
  N8: IC1.pin14, J1.pin1, J1.pin2, 3_3V_reg.input_voltage, R2.Pin_0, R3.Pin_0, R4.Pin_0, C1.-, part.1, REV_Relay.connector0, REV_Relay.connector2, FWD_Relay.connector0, FWD_Relay.connector2, D1.cathode, D2.cathode, Q1.E, Q1.C, Q2.E, Q2.C, Forward_2.anode, Reverse_2.anode, Pressure.anode, Fuse.pin_1, Fuse.pin_2
  N9: Solenoids.pin1, FWD_Relay.connector3
  N10: Solenoids.pin2, REV_Relay.connector3
  N11: 3_3V_reg.output_voltage, J5.pin2, C1.+
  N12: R5.Pin_1, R6.Pin_1, Q1.B, Q2.B
  N13: Forward_2.cathode, R11.Pin_0
  N14: Reverse_2.cathode, R10.Pin_0
  N15: Pressure.cathode, R9.Pin_0
  N16: R12.Pin_0, R13.Pin_0

notes:
  P1_5
  P1_4
  P1_3
  12V
  GND
  120V
  REV
  FWD
  N
  Hydraulic Auto-Reverse
  V 2.0
  MSP430
  PSI
  Hydraulic Auto-Reverse V 2.0
  3.3DC
