# Fritzing sketch id2222_LampkaNocna_0 (saved by Fritzing 0.9.2b)
breadboards: 1

parts:
  Part1 = Arduino Uno (Rev3)
  R1 = PHOTOCELL [package=photocell-kit]
  LED1 = smd LED [color="Red (633nm)" package="0805 [SMD]"]
  R2 = Resistor [tolerance=±1% resistance=10k package=THT]
  R3 = Resistor [tolerance=±1% resistance=10k package=THT]

nets:
  N1: Part1.A0, R1.P$2, R2.Pin_0
  N2: Part1.D13/SCK, R3.Pin_1
  N3: Part1.5V, R1.P$1
  N4: Part1.GND, LED1.cathode, R2.Pin_1
  N5: LED1.anode, R3.Pin_0

notes:
  REZYSTOR:
  10kΩ - np.
  brązowy, czarny, czarny, czerwony, brązowy
  ↓
