# Fritzing sketch id2223_Lamp_Project_0 (saved by Fritzing 0.9.2b)
breadboards: 1

parts:
  Part1 = Arduino Uno (Rev3)
  R3 = Resistor [tolerance=±5% resistance=220 package=THT]
  R4 = Resistor [tolerance=±5% resistance=220 package=THT]
  R5 = Resistor [tolerance=±5% resistance=220 package=THT]
  LED1 = RGB LED (com. cathode, rgb) [package="5 mm [THT]"]
  R6 = Resistor [tolerance=±5% resistance=10k package=THT]
  R7 = Resistor [tolerance=±5% resistance=10k package=THT]
  R8 = Resistor [tolerance=±5% resistance=10k package=THT]
  R9 = Photocell (LDR) [package=THT]
  R10 = Photocell (LDR) [package=THT]
  R11 = Photocell (LDR) [package=THT]

nets:
  N1: Part1.A0, R8.Pin_0, R11.pin_1
  N2: Part1.A1, R6.Pin_0, R9.pin_1
  N3: Part1.A2, R7.Pin_0, R10.pin_1
  N4: Part1.D9_PWM, R5.Pin_1
  N5: Part1.D10_PWM/SS, R4.Pin_1
  N6: Part1.D11_PWM/MOSI, R3.Pin_0
  N7: Part1.5V, R9.pin_0, R10.pin_0, R11.pin_0
  N8: Part1.GND, LED1.common_cathode, R6.Pin_1, R7.Pin_1, R8.Pin_1
  N9: R3.Pin_1, LED1.blue_anode
  N10: R4.Pin_0, LED1.green_anode
  N11: R5.Pin_0, LED1.red_anode
