# Fritzing sketch id2224_lampka_0 (saved by Fritzing 0.9.3b)
circuit board: 2.2cm x 1cm
breadboards: 1

parts:
  R1 = Resistor [tolerance=±5% resistance=1k package=THT]
  Q1 = Basic FET N-Channel [package="TO220 [THT]"]
  PIN = female pin header, 3 pins [form="♀ (female)"]

nets:
  N1: R1.Pin_0, PIN.pin1
  N2: R1.Pin_1, Q1.gate
  N3: Q1.drain, PIN.pin2
  GND: Q1.source, PIN.pin3
