# Fritzing sketch id2225_Lampadina_0 (saved by Fritzing 0.9.2b)
circuit board: 8.46667cm x 5.64444cm
breadboards: 1

parts:
  Componente1 = Arduino Uno (Rev3)
  VCC1 = Battery
  Q1 = NPN-Transistor [package="TO92 [THT]"]
  LED1 = LED - 5mm [color="Red (633nm)" package="5 mm [THT]"]
  J1 = Piezo Speaker
  R1 = Resistor [tolerance=±5% resistance=220 package=THT]
  R2 = Photocell (LDR) [package=THT]
  R3 = Resistor [tolerance=±5% resistance=220 package=THT]
  R4 = Resistor [tolerance=±5% resistance=220 package=THT]

nets:
  N1: Componente1.A0, R2.pin_1, R3.Pin_0
  N2: Componente1.A1, Componente1.5V, VCC1.+, R3.Pin_1
  N3: Componente1.GND, VCC1.-, Q1.C, LED1.cathode, J1.pin1, R2.pin_0
  N4: Componente1.D2, R1.Pin_0
  N5: Componente1.D3_PWM, R4.Pin_1
  N6: Q1.E, R1.Pin_1
  N7: Q1.B, J1.pin2
  N8: LED1.anode, R4.Pin_0
