# Fritzing sketch id2227_LANC_0 (saved by Fritzing 0.9.3b)
breadboards: 1

parts:
  Part1 = Arduino Uno (Rev3)
  U1 = 3.5mm Audio Jack [package=audio-jack-3.5mm-smd]
  D1 = Zener Diode [part_number=1N4732A breakdown_voltage=5.1V package="300 mil [THT]"]
  R1 = Resistor [tolerance=±2% resistance=4.7k package="2512 [SMD]"]
  Q1 = TRANSISTOR_NPN [package=to-92]
  R2 = Resistor [tolerance=±5% resistance=5.6k package="2512 [SMD]"]

nets:
  N1: Part1.D11_PWM/MOSI, U1.LEFT, D1.cathode, R1.Pin_0, Q1.C
  N2: Part1.GND, U1.SLEEVE, D1.anode, Q1.E
  N3: Part1.D7, R2.Pin_0
  N4: Part1.5V, U1.RIGHT, R1.Pin_1
  N5: Q1.B, R2.Pin_1
