# Fritzing sketch id2228_SLS_controller_SMD_0 (saved by Fritzing 0.7.11b)
breadboards: 1

parts:
  S1 = Toggle Switch [package=THT]
  U1 = Voltage Regulator - 5V [package="TO220 [THT]"]
  R1 = Resistor [tolerance=±5% resistance=3k package="0805 [SMD]"]
  R2 = Resistor [tolerance=±5% resistance=1k package="0805 [SMD]"]
  Q1 = NPN-Transistor [package="SOT-23 [SMD]"]
  13_8V_in = Pad [width=1.75 height=1.75 connect=center]
  GND = Pad [width=1.75 height=1.75 connect=center]
  O/P = Pad [width=1.75 height=1.75 connect=center]
  Down = Pad [width=1.75 height=1.75 connect=center]
  Up = Pad [width=1.75 height=1.75 connect=center]
  Switch_GND = Pad [width=1.75 height=1.75 connect=center]
  Arduino = Arduino Pro Mini 3.3V

nets:
  N1: S1.L1, Up.pad, Arduino.MOSI
  GND: S1.COM, U1.GND, Q1.2, GND.pad, Switch_GND.pad, Arduino.GND
  N2: S1.L2, Down.pad, Arduino.D10
  12V: U1.input_voltage, R2.Pin_1, 13_8V_in.pad
  N3: U1.output_voltage, Arduino.VCC
  N4: R1.Pin_0, Arduino.MISO
  N5: R1.Pin_1, Q1.0
  N6: R2.Pin_0, Q1.1, O/P.pad

notes:
  SLS v1.0
