# Fritzing sketch id2229_SLS_controller_0 (saved by Fritzing 0.7.11b)
breadboards: 1

parts:
  R1 = Resistor [tolerance=±5% resistance=3k package=THT]
  Q1 = NPN-Transistor [part_number=BC501 package="TO92 [THT]"]
  R2 = Resistor [tolerance=±5% resistance=1k package=THT]
  S1 = Toggle Switch [package=THT]
  U1 = Voltage Regulator - 5V [package="TO220 [THT]"]
  13_8V_in = Pad [width=1.75 height=1.75 connect=center]
  O/P = Pad [width=1.75 height=1.75 connect=center]
  Down = Pad [width=1.75 height=1.75 connect=center]
  Up = Pad [width=1.75 height=1.75 connect=center]
  Switch_GND = Pad [width=1.75 height=1.75 connect=center]
  Part1 = Arduino Pro Mini 3.3V
  GND = Pad [width=1.75 height=1.75 connect=center]

nets:
  N1: R1.Pin_0, Part1.MISO
  N2: R1.Pin_1, Q1.B
  GND: Q1.E, S1.COM, U1.GND, Switch_GND.pad, Part1.GND, GND.pad
  N3: Q1.C, R2.Pin_0, O/P.pad
  12V: R2.Pin_1, U1.input_voltage, 13_8V_in.pad
  N4: S1.L1, Up.pad, Part1.MOSI
  N5: S1.L2, Down.pad, Part1.D10
  N6: U1.output_voltage, Part1.VCC

notes:
  SLS v1.0
