# Fritzing sketch id2230_Untitled_Sketch_0 (saved by Fritzing 0.9.3b)
breadboards: 1

parts:
  R1 = Photocell (LDR) [package=THT]
  R2 = Resistor [tolerance=±5% resistance=220 package=THT]
  Q1 = NPN-Transistor [package="TO92 [THT]"]
  J1 = Piezo Speaker
  R3 = Resistor [tolerance=±5% resistance=220 package=THT]
  BAT1 = Battery Holders [package=battery-aa-kit]

nets (from the breadboard view):
  N1: R1.pin_0, R2.Pin_0, J1.pin2
  N2: R1.pin_1, Q1.C, J1.pin1
  N3: R2.Pin_1, BAT1.+
  N4: Q1.E, R3.Pin_0
  N5: Q1.B, BAT1.-
