# Fritzing sketch id2231_Laser_Alarm_Project_0 (saved by Fritzing 0.7.12b)
breadboards: 1

parts:
  R1 = Photocell (LDR) [package=THT]
  Arduino1 = Arduino
  R2 = 10k Ω Resistor [package=THT]
  LED1 = Blue LED - 5mm [package="5 mm [THT]"]
  R3 = Rotary Potentiometer (Small) [maximum_resistance=100kΩ]  # not connected

nets:
  N1: R1.pin_1, Arduino1.+5V
  N2: Arduino1.D12, LED1.cathode
  N3: Arduino1.D11, LED1.anode
  N4: Arduino1.GND, R2.Pin_1

notes:
  Laser Alarm Project
  Laser point
  i know it's not a laser point but consider it laser point, because there is no laser image on that program .
  Tools :
  =====
  1) Arduino, (anything).
  2) LED Light .
  3) Resistor .
  4) photocell .
  5) Laser Point .
  6) Breadboard .
  Laser Line >>
