# Fritzing sketch id2232_Laser_Gun_Receiver_0 (saved by Fritzing 0.9.3b)
stripboards: 1

parts:
  Part1 = Arduino Uno (Rev3)
  R2 = Photocell (LDR) [package=THT]
  DI3 = 7-Segment LED Display [package=THT]
  DI4 = 7-Segment LED Display [package=THT]
  J3 = Screw terminal - 2 pins [package=THT]
  U1 = POT [package=alps_pot]
  J5 = Screw terminal - 2 pins [package=THT]
  J6 = Screw terminal - 2 pins [package=THT]
  J7 = Screw terminal - 2 pins [package=THT]
  R3 = Resistor [tolerance=±5% resistance=220 package=THT]
  R4 = Resistor [tolerance=±5% resistance=220 package=THT]
  R5 = Resistor [tolerance=±5% resistance=220 package=THT]
  R6 = Resistor [tolerance=±5% resistance=220 package=THT]
  J8 = Screw terminal - 2 pins [package=THT]
  J9 = Screw terminal - 2 pins [package=THT]
  R7 = Resistor [tolerance=±5% resistance=220 package=THT]
  R8 = Resistor [tolerance=±5% resistance=220 package=THT]
  R9 = Resistor [tolerance=±5% resistance=220 package=THT]
  R10 = Resistor [tolerance=±5% resistance=220 package=THT]
  J11 = Screw terminal - 2 pins [package=THT]
  J12 = Screw terminal - 2 pins [package=THT]
  J13 = Screw terminal - 2 pins [package=THT]
  J14 = Screw terminal - 2 pins [package=THT]
  J4 = Basic Servo

nets:
  N1: Part1.D8, R3.Pin_1, J8.pin1
  N2: Part1.D9_PWM, R6.Pin_1, J8.pin2
  N3: Part1.D10_PWM/SS, J4.pulse
  N4: Part1.D11_PWM/MOSI, DI4.commAnode#7, J14.pin1
  N5: Part1.D12/MISO, DI3.commAnode#7, J14.pin2
  GND: Part1.GND, R2.pin_0, J3.pin2, J5.pin2, J6.pin1, J6.pin2, J4.gnd
  N6: Part1.D2, R2.pin_1, J3.pin1, U1.S, J13.pin2
  N7: Part1.D3_PWM, R4.Pin_1, J9.pin2
  N8: Part1.D4, R5.Pin_1, J9.pin1
  N9: Part1.D5_PWM, R8.Pin_1, J12.pin1
  N10: Part1.D6_PWM, R7.Pin_1, J11.pin2
  N11: Part1.D7, R10.Pin_1, J11.pin1
  5V: Part1.5V, U1.E, J5.pin1, J7.pin1, J7.pin2, J4.vcc
  N12: DI3.cathodeE, DI4.cathodeE, R10.Pin_0
  N13: DI3.cathodeD, DI4.cathodeD, R7.Pin_0
  N14: DI3.cathodeC, DI4.cathodeC, R8.Pin_0
  N15: DI3.cathodeDP, DI4.cathodeDP, R9.Pin_0
  N16: DI3.cathodeB, DI4.cathodeB, R5.Pin_0
  N17: DI3.cathodeA, DI4.cathodeA, R4.Pin_0
  N18: DI3.cathodeF, DI4.cathodeF, R3.Pin_0
  N19: DI3.cathodeG, DI4.cathodeG, R6.Pin_0
  N20: U1.A, J13.pin1
  N21: R9.Pin_1, J12.pin2

notes:
  G  F  A  B
  E  D  C  Dot
