# Fritzing sketch id2234_Laser_Tag_Target_0 (saved by Fritzing 0.9.3b)
breadboards: 1

parts:
  Part1 = Arduino Nano (Rev3.0)
  R1 = Resistor [tolerance=±5% resistance=1k package="0805 [SMD]"]
  R2 = Resistor [tolerance=±5% resistance=1k package="0805 [SMD]"]
  R3 = Resistor [tolerance=±5% resistance=2k package="0805 [SMD]"]
  R4 = PHOTOCELL [package=photocell]
  J1 = Piezo Speaker
  S1 = Toggle Switch [package=THT]
  Q1 = NPN-Transistor [package="TO92 [THT]"]
  VCC1 = Battery block 9V
  Q2 = NPN-Transistor [package="TO92 [THT]"]
  LED1 = LED - 3mm [color="Red (633nm)" package="3 mm [THT]"]
  LED2 = LED - 3mm [color="Red (633nm)" package="3 mm [THT]"]
  LED3 = LED - 3mm [color="Red (633nm)" package="3 mm [THT]"]
  LED4 = LED - 3mm [color="Red (633nm)" package="3 mm [THT]"]
  LED5 = LED - 3mm [color="Red (633nm)" package="3 mm [THT]"]
  LED6 = LED - 3mm [color="Red (633nm)" package="3 mm [THT]"]
  LED7 = LED - 3mm [color="Blue (430nm)" package="3 mm [THT]"]
  LED8 = LED - 3mm [color="Blue (430nm)" package="3 mm [THT]"]
  LED9 = LED - 3mm [color="Blue (430nm)" package="3 mm [THT]"]
  LED10 = LED - 3mm [color="Blue (430nm)" package="3 mm [THT]"]
  LED11 = LED - 3mm [color="Blue (430nm)" package="3 mm [THT]"]
  LED12 = LED - 3mm [color="Blue (430nm)" package="3 mm [THT]"]
  R5 = Resistor [tolerance=±5% resistance=220 package="0805 [SMD]"]
  R6 = Resistor [tolerance=±5% resistance=220 package="0805 [SMD]"]
  R7 = Resistor [tolerance=±5% resistance=220 package="0805 [SMD]"]
  R8 = Resistor [tolerance=±5% resistance=220 package="0805 [SMD]"]
  R9 = Resistor [tolerance=±5% resistance=220 package="0805 [SMD]"]  # not connected
  R10 = Resistor [tolerance=±5% resistance=220 package="0805 [SMD]"]
  R11 = Resistor [tolerance=±5% resistance=220 package="0805 [SMD]"]
  R12 = Resistor [tolerance=±5% resistance=220 package="0805 [SMD]"]
  R13 = Resistor [tolerance=±5% resistance=220 package="0805 [SMD]"]
  R14 = Resistor [tolerance=±5% resistance=220 package="0805 [SMD]"]
  R15 = Resistor [tolerance=±5% resistance=220 package="0805 [SMD]"]
  R16 = Resistor [tolerance=±5% resistance=220 package="0805 [SMD]"]
  R17 = Resistor [tolerance=±5% resistance=220 package="0805 [SMD]"]

nets:
  N1: Part1.GND, R3.Pin_0, J1.pin1, Q1.C, VCC1.-, Q2.C
  N2: Part1.D5, J1.pin2
  N3: Part1.D10, R2.Pin_1
  N4: Part1.D11/MOSI, R1.Pin_1
  N5: Part1.VIN, S1.COM
  N6: Part1.A4, R3.Pin_1, R4.P$1
  N7: Part1.3V3, R4.P$2
  N8: R1.Pin_0, Q2.E, R17.Pin_1
  N9: R2.Pin_0, Q1.E, R16.Pin_1
  N10: S1.L2, VCC1.+
  N11: Q1.B, LED1.cathode, LED2.cathode, LED3.cathode, LED4.cathode, LED5.cathode, LED6.cathode
  N12: Q2.B, LED7.cathode, LED8.cathode, LED9.cathode, LED10.cathode, LED11.cathode, LED12.cathode
  N13: LED1.anode, R6.Pin_0, R7.Pin_1
  N14: LED2.anode, R8.Pin_0, R10.Pin_0
  N15: LED3.anode, R5.Pin_0, R6.Pin_1
  N16: LED4.anode, R10.Pin_1, R16.Pin_0
  N17: LED5.anode, R5.Pin_1
  N18: LED6.anode, R7.Pin_0, R8.Pin_1
  N19: LED7.anode, R13.Pin_1
  N20: LED8.anode, R12.Pin_0, R14.Pin_1
  N21: LED9.anode, R12.Pin_1, R15.Pin_0
  N22: LED10.anode, R13.Pin_0, R14.Pin_0, R17.Pin_0
  N23: LED11.anode, R11.Pin_1, R15.Pin_1
  N24: LED12.anode, R11.Pin_0
