# Fritzing sketch id2236_Laser_Leonardo_0 (saved by Fritzing 0.8.7b)

parts:
  KY-008_Laserdiode1 = keys0000 [part_number=1219301]
  Bauteil1 = Arduino Leonardo (Rev3b)
  R1 = Resistor [tolerance=±5% resistance=330 package=THT]

nets:
  N1: KY-008_Laserdiode1.connector2, R1.Pin_1
  N2: KY-008_Laserdiode1.connector3, Bauteil1.5V
  N3: KY-008_Laserdiode1.connector4, Bauteil1.GND
  N4: Bauteil1.D10_PWM/A10, R1.Pin_0
