# Fritzing sketch id2237_Laser_Nano3_0 (saved by Fritzing 0.8.7b)

parts:
  KY-008_Laserdiode1 = keys0000 [part_number=1219301]
  R1 = Resistor [tolerance=±5% resistance=330 package=THT]
  Bauteil2 = Arduino Nano (Rev3.0)

nets:
  N1: KY-008_Laserdiode1.connector2, R1.Pin_1
  N2: KY-008_Laserdiode1.connector3, Bauteil2.RESET, Bauteil2.5V
  VIN: KY-008_Laserdiode1.connector4, Bauteil2.VIN, Bauteil2.GND
  N3: R1.Pin_0, Bauteil2.3V3, Bauteil2.D13/SCK
