# Fritzing sketch id2238_Laser_0 (saved by Fritzing 0.8.3b)
circuit board: 16.9333cm x 5.64444cm
breadboards: 1

parts:
  Part1 = Arduino Uno (Rev3)
  LED1 = smd LED [color="Red (633nm)" package="0805 [SMD]"]
  R1 = Resistor [tolerance=±5% resistance=220 package=THT]
  Q1 = NPN-Transistor [part_number=BC237 package="SOT-23 [SMD]"]
  R2 = Resistor [tolerance=±5% resistance=680 package=THT]
  C2 = Electrolytic Capacitor [capacitance=1µF package="100 mil [THT, electrolytic]"]
  U1 = Voltage Regulator [package=to220-adj]
  R3 = Photocell (LDR) [package=THT]
  R4 = Resistor [tolerance=±5% resistance=10k package=THT]
  D1 = Rectifier Diode [part_number=1N4001 package="300 mil [THT]"]
  U2 = 74HC595 [package="DIP16 [THT]"]
  7_Segment2 = 7 Segment Display
  7_Segment1 = 7 Segment Display
  U3 = 74HC595 [package="DIP16 [THT]"]
  JP1 = Header 2 [part_number="J1 - Canon 2.5mm Plug" package=molex-1x2_lock]
  S1 = SWITCH-MOMENTARY-2 [package=tactile-pth]
  S2 = SWITCH-MOMENTARY-2 [part_number="Switch - UP" package=tactile-pth]
  R5 = Resistor [tolerance=±5% resistance=10k package=THT]
  JP2 = Header 2 [part_number="J2 - Laser" package=molex-1x2_lock]
  S3 = SWITCH-MOMENTARY-2 [package=tactile-pth]
  R6 = Resistor [tolerance=±5% resistance=10k package=THT]
  R7 = Resistor [tolerance=±5% resistance=10k package=THT]

nets:
  N1: Part1.A0, R3.pin_0, R4.Pin_1
  GND: Part1.GND, LED1.cathode, Q1.1, C2.-, R3.pin_1, D1.anode, U2.OE, 7_Segment2.common_cathode, 7_Segment1.common_cathode, U3.GND, U3.OE, JP1.2, R5.Pin_0, JP2.1, R6.Pin_0, R7.Pin_0
  N2: Part1.D8, U2.DS
  N3: Part1.D9_PWM, Q1.0
  N4: Part1.D13/SCK, R2.Pin_1
  N5: Part1.D6_PWM, U2.SH_CP, U3.SH_CP
  N6: Part1.D7, U2.ST_CP, U3.ST_CP
  VCC: Part1.5V, U1.OUT, R4.Pin_0, U2.MR, U2.VCC, U3.MR, U3.VCC, S1.2, S2.2, S3.2
  N7: LED1.anode, R2.Pin_0
  N8: R1.Pin_0, C2.+, U1.ADJ, D1.cathode, JP2.2
  N9: R1.Pin_1, U1.IN
  N10: Q1.2, JP1.1
  N11: U2.Q1, 7_Segment1.Segment_A#10
  N12: U2.Q2, 7_Segment1.Segment_B
  N13: U2.Q3, 7_Segment1.Segment_C
  N14: U2.Q4, 7_Segment1.Segment_D
  N15: U2.Q5, 7_Segment1.Segment_E
  N16: U2.Q6, 7_Segment1.Segment_F
  N17: U2.Q7', U3.DS
  N18: U2.Q0, 7_Segment1.Segment_A#1
  N19: 7_Segment2.Segment_A#1, 7_Segment2.Segment_F, U3.Q6, U3.Q0
  N20: 7_Segment2.Segment_E, U3.Q5
  N21: 7_Segment2.Segment_D, U3.Q4
  N22: 7_Segment2.Segment_C, U3.Q3
  N23: 7_Segment2.Segment_B, U3.Q2
  N24: 7_Segment2.Segment_A#10, U3.Q1
  N25: S1.1, R5.Pin_1
  N26: S2.1, R6.Pin_1
  N27: S3.1, R7.Pin_1

notes:
  Start/Stop
  Down
  Up
  Canon
  2.5mm conn.
  Laser
  Diode
  Laser Trigger project for Canon Camera
  http://blog.gjmccarthy.co.uk
