# Fritzing sketch id2239_LaserTurret_0 (saved by Fritzing 0.9.3b)
breadboards: 1

parts:
  S1 = Pushbutton [package="[THT]"]
  S2 = Pushbutton [package="[THT]"]
  S3 = Pushbutton [package="[THT]"]
  RE1 = Rotary Encoder [package=THT]
  7_Segment1 = 7 Segment Display
  U1 = 74HC595 [package="DIP16 [THT]"]
  Bauteil1 = Arduino Uno (Rev3)
  LED1 = LED - 5mm [color="Red (633nm)" package="5 mm [THT]"]
  LED2 = LED - 5mm [color="Red (633nm)" package="5 mm [THT]"]
  J3 = Basic Servo
  R1 = Resistor [tolerance=±5% resistance=220 package=THT]
  R2 = Resistor [tolerance=±5% resistance=220 package=THT]
  J4 = Basic Servo

nets:
  N1: S1.Pin_1, S1.Pin_2, Bauteil1.D4
  GND: S1.Pin_3, S1.Pin_4, S2.Pin_3, S2.Pin_4, S3.Pin_3, S3.Pin_4, U1.OE, Bauteil1.GND, J3.gnd, R1.Pin_1, R2.Pin_1, J4.gnd
  N2: S2.Pin_1, S2.Pin_2, Bauteil1.D3_PWM
  N3: S3.Pin_1, S3.Pin_2, Bauteil1.D2
  N4: RE1.EncoderPinA, Bauteil1.D6_PWM
  N5: RE1.EncoderPinC, Bauteil1.D7
  VCC: RE1.EncoderPinB, U1.MR, U1.VCC, Bauteil1.5V, J3.vcc, J4.vcc
  N6: 7_Segment1.Segment_G, U1.Q2
  N7: 7_Segment1.Segment_F, U1.Q1
  N8: 7_Segment1.common_anode, R2.Pin_0
  N9: 7_Segment1.Segment_E, U1.Q6
  N10: 7_Segment1.Segment_D, U1.Q7
  N11: 7_Segment1.Segment_DP, U1.Q5
  N12: 7_Segment1.Segment_C, U1.Q4
  N13: 7_Segment1.Segment_B, U1.Q3
  N14: U1.SH_CP, Bauteil1.D10_PWM/SS
  N15: U1.ST_CP, Bauteil1.D9_PWM
  N16: U1.DS, Bauteil1.D8
  N17: Bauteil1.A0, J3.pulse
  N18: Bauteil1.A1, J4.pulse
  N19: Bauteil1.A2, LED2.cathode
  N20: Bauteil1.D11_PWM/MOSI, LED1.cathode
  N21: LED1.anode, R1.Pin_0
