# Fritzing sketch id223_accLogger_0 (saved by Fritzing 0.9.1b)
circuit board: 8.46667cm x 5.64444cm
breadboards: 1

parts:
  Part1 = Triple Axis Accelerometer Breakout - ADXL335
  microSD_Transflash1 = SparkFun - microSD Transflash
  Part2 = Arduino Nano (Rev3.0)

nets:
  N1: Part1.ZOUT, Part2.A0
  N2: Part1.YOUT, Part2.A1
  N3: Part1.XOUT, Part2.A2
  GND: Part1.GND, microSD_Transflash1.GND, Part2.GND
  VCC: Part1.VCC, microSD_Transflash1.VCC, Part2.5V
  N4: microSD_Transflash1.DO, Part2.D11/MOSI
  N5: microSD_Transflash1.SCK, Part2.D13/SCK
  N6: microSD_Transflash1.DI, Part2.D12/MISO
  N7: microSD_Transflash1.CS, Part2.D4
