# Fritzing sketch id2240_latch_halleffect_lcd_0 (saved by Fritzing 0.8.7b)
breadboards: 1

parts:
  LCD1 = LCD screen
  R1 = Trimmer Potentiometer [maximum_resistance=10kΩ package=THT]
  U1 = HALL-EFFECT [package=sc70]
  Part2 = Arduino Uno (Rev3)

nets:
  GND: LCD1.VSS, LCD1.R/W, LCD1.LED-, R1.leg2, U1.GND, Part2.GND
  VDD: LCD1.VDD, LCD1.LED+, R1.leg1, Part2.5V
  N1: LCD1.RS, Part2.D7
  N2: LCD1.E, Part2.D8
  N3: LCD1.DB4, Part2.D9_PWM
  N4: LCD1.DB6, Part2.D11_PWM/MOSI
  N5: LCD1.DB7, Part2.D12/MISO
