# Fritzing sketch id2242_Lauflicht_6_LED_6Schalter_0 (saved by Fritzing 0.7.11b)
breadboards: 1

parts:
  Arduino1 = Arduino
  R1 = Resistor [tolerance=±5% resistance=150 package=THT]
  R2 = Resistor [tolerance=±5% resistance=150 package=THT]
  R3 = Resistor [tolerance=±5% resistance=150 package=THT]
  R4 = Resistor [tolerance=±5% resistance=150 package=THT]
  R5 = Resistor [tolerance=±5% resistance=150 package=THT]
  LED1 = LED - 5mm [color="Red (633nm)" package="5 mm [THT]"]
  LED2 = LED - 5mm [color="Red (633nm)" package="5 mm [THT]"]
  LED3 = LED - 5mm [color="Red (633nm)" package="5 mm [THT]"]
  LED4 = LED - 5mm [color="Red (633nm)" package="5 mm [THT]"]
  LED5 = LED - 5mm [color="Red (633nm)" package="5 mm [THT]"]
  LED6 = LED - 5mm [color="Red (633nm)" package="5 mm [THT]"]
  S1 = Pushbutton [package=THT]
  S2 = Pushbutton [package=THT]
  S3 = Pushbutton [package=THT]
  S4 = Pushbutton [package=THT]
  S5 = Pushbutton [package=THT]
  S6 = Pushbutton [package=THT]
  R6 = Resistor [tolerance=±5% resistance=10k package=THT]
  R7 = Resistor [tolerance=±5% resistance=10k package=THT]
  R8 = Resistor [tolerance=±5% resistance=10k package=THT]
  R9 = Resistor [tolerance=±5% resistance=10k package=THT]
  R10 = Resistor [tolerance=±5% resistance=10k package=THT]
  R11 = Resistor [tolerance=±5% resistance=10k package=THT]

nets (from the pcb view):
  N1: Arduino1.GND, LED1.cathode, LED2.cathode, LED3.cathode, LED4.cathode, LED5.cathode, LED6.cathode, R6.Pin_1, R7.Pin_1, R8.Pin_1, R9.Pin_1, R10.Pin_1, R11.Pin_1
  N2: Arduino1.D13, LED6.anode
  N3: Arduino1.D12, R1.Pin_1
  N4: Arduino1.D11, R2.Pin_1
  N5: Arduino1.D10, R3.Pin_1
  N6: Arduino1.D9, R4.Pin_1
  N7: Arduino1.D8, R5.Pin_1
  N8: Arduino1.D7, S1.leg1, R6.Pin_0
  N9: Arduino1.D6, S2.leg1, R7.Pin_0
  N10: Arduino1.D5, S3.leg1, R8.Pin_0
  N11: Arduino1.D4, S4.leg1, R9.Pin_0
  N12: Arduino1.D3, S5.leg1, R10.Pin_0
  N13: Arduino1.D2, S6.leg1, R11.Pin_0
  N14: Arduino1.+5V, S1.leg0, S2.leg0, S3.leg0, S4.leg0, S5.leg0, S6.leg0
  N15: R1.Pin_0, LED1.anode
  N16: R2.Pin_0, LED2.anode
  N17: R3.Pin_0, LED3.anode
  N18: R4.Pin_0, LED4.anode
  N19: R5.Pin_0, LED5.anode

notes:
  FTE
  GWS Lörrach
