# Fritzing sketch id2243_Lauflicht_Projekt_0 (saved by Fritzing 0.9.3b)
circuit board: 8.46667cm x 5.64444cm
breadboards: 1

parts:
  LED1 = LED - 5mm [color="Red (633nm)" package="5 mm [THT]"]
  LED2 = LED - 5mm [color="Red (633nm)" package="5 mm [THT]"]
  LED3 = LED - 5mm [color="Red (633nm)" package="5 mm [THT]"]
  LED4 = LED - 5mm [color="Red (633nm)" package="5 mm [THT]"]
  LED5 = LED - 5mm [color="Red (633nm)" package="5 mm [THT]"]
  LED6 = LED - 5mm [color="Red (633nm)" package="5 mm [THT]"]
  R1 = Resistor [tolerance=±5% resistance=220 package=THT]
  R2 = Resistor [tolerance=±5% resistance=220 package=THT]
  R3 = Resistor [tolerance=±5% resistance=220 package=THT]
  R4 = Resistor [tolerance=±5% resistance=220 package=THT]
  R5 = Resistor [tolerance=±5% resistance=220 package=THT]
  R6 = Resistor [tolerance=±5% resistance=220 package=THT]
  RE1 = Rotary Encoder [package=THT]
  Lauflicht = Arduino Uno (Rev3)

nets:
  N1: LED1.cathode, LED2.cathode, LED3.cathode, LED4.cathode, LED5.cathode, LED6.cathode, RE1.EncoderPinB, Lauflicht.GND
  N2: LED1.anode, R1.Pin_1
  N3: LED2.anode, R2.Pin_1
  N4: LED3.anode, R3.Pin_1
  N5: LED4.anode, R4.Pin_1
  N6: LED5.anode, R5.Pin_1
  N7: LED6.anode, R6.Pin_1
  N8: R1.Pin_0, Lauflicht.D13/SCK
  N9: R2.Pin_0, Lauflicht.D12/MISO
  N10: R3.Pin_0, Lauflicht.D11_PWM/MOSI
  N11: R4.Pin_0, Lauflicht.D10_PWM/SS
  N12: R5.Pin_0, Lauflicht.D9_PWM
  N13: R6.Pin_0, Lauflicht.D8
  N14: RE1.EncoderPinA, Lauflicht.5V
  N15: RE1.EncoderPinC, Lauflicht.A0
