# Fritzing sketch id2244_Lauflicht_Poti_0 (saved by Fritzing 0.9.2b)
breadboards: 1

parts:
  Arduino_Uno = Arduino Uno (Rev3)
  Rot = LED - 5mm [color="Red (633nm)" package="5 mm [THT]"]
  Gelb = LED - 5mm [color="Yellow (595nm)" package="5 mm [THT]"]
  Blau = LED - 5mm [color="Blue (470nm)" package="5 mm [THT]"]
  Grün = LED - 5mm [color="Green (560nm)" package="5 mm [THT]"]
  R1 = Resistor [tolerance=±5% resistance=220 package=THT]
  R2 = Resistor [tolerance=±5% resistance=220 package=THT]
  R3 = Resistor [tolerance=±5% resistance=220 package=THT]
  R4 = Resistor [tolerance=±5% resistance=220 package=THT]
  R5 = TRIMPOT [package=trimpot_pth_s3_lock]

nets:
  N1: Arduino_Uno.A0, R5.WIPER
  N2: Arduino_Uno.D10_PWM/SS, R3.Pin_1
  N3: Arduino_Uno.D11_PWM/MOSI, R2.Pin_1
  N4: Arduino_Uno.D12/MISO, R1.Pin_1
  N5: Arduino_Uno.GND, Rot.cathode, Gelb.cathode, Blau.cathode, Grün.cathode, R5.CCW
  N6: Arduino_Uno.D3_PWM, R4.Pin_1
  N7: Arduino_Uno.5V, R5.CW
  N8: Rot.anode, R1.Pin_0
  N9: Gelb.anode, R2.Pin_0
  N10: Blau.anode, R4.Pin_0
  N11: Grün.anode, R3.Pin_0
