# Fritzing sketch id2245_Laura_0 (saved by Fritzing 0.9.0b)
breadboards: 1

parts:
  C5 = 22pf
  C6 = 22pf
  XTAL3 = Crystal [frequency="16 Mhz" package=THT]
  Componente4 = Triple Axis Magnetometer - HMC5883 Breakout
  R3 = Resistor [tolerance=±5% resistance=1k package=THT]
  NEOPIXEL3 = Neopixel_Strip____Black__30_m
  CONN3 = usb micro
  U2 = atmega328 [package=dip]
  S1 = Pushbutton [package=THT]

nets:
  GND: C5.connector0, C6.connector1, Componente4.GND, NEOPIXEL3.connector3, CONN3.connector3, U2.GND, S1.leg1
  N1: C5.connector1, XTAL3.pin_0, U2.XLAT1
  N2: C6.connector0, XTAL3.pin_1, U2.XLAT2
  VCC: Componente4.VCC, NEOPIXEL3.connector1, CONN3.connector0, U2.VCC, U2.AVCC
  N3: Componente4.SDA, U2.A4
  N4: Componente4.SCL, U2.A5
  N5: R3.Pin_0, NEOPIXEL3.connector2
  N6: R3.Pin_1, U2.D9_(PWM)
  N7: U2.D8, S1.leg0
