# Fritzing sketch id2246_Filter_V2_0 (saved by Fritzing 0.9.2b)
breadboards: 1

parts:
  C1 = Ceramic Capacitor [capacitance=100nF package="100 mil [THT, multilayer]"]
  R1 = Resistor [tolerance=±5% resistance=220 package=THT]
  L1 = Inductor [package="400 mil [THT]"]
  R2 = Resistor [tolerance=±5% resistance=220 package=THT]
  C2 = Ceramic Capacitor [capacitance=100nF package="100 mil [THT, multilayer]"]
  L2 = Inductor [package="400 mil [THT]"]
  C3 = Ceramic Capacitor [capacitance=100nF package="100 mil [THT, multilayer]"]
  R3 = Resistor [tolerance=±5% resistance=220 package=THT]
  R4 = Resistor [tolerance=±5% resistance=220 package=THT]

nets:
  N1: C1.0, R1.Pin_1
  N2: C1.1, L1.pin_1
  N3: R1.Pin_0, L1.pin_0
  N4: R2.Pin_0, C2.1
  N5: R2.Pin_1, R4.Pin_0
  N6: C2.0, L2.pin_0, C3.1
  N7: C3.0, R3.Pin_1
  N8: R3.Pin_0, R4.Pin_1
