# Fritzing sketch id2249_LCD_Brightness_contrass_0 (saved by Fritzing 0.9.1b)
circuit board: 8.46667cm x 5.64444cm
breadboards: 1

parts:
  LCD1 = LCD screen
  Part1 = Arduino Uno (Rev3)
  R1 = Resistor [tolerance=±5% resistance=10k package=THT]
  R2 = Rotary Potentiometer (Small) [maximum_resistance=10kΩ package=THT]
  R3 = Rotary Potentiometer (Small) [maximum_resistance=1kΩ package=THT]

nets:
  VSS: LCD1.VSS, LCD1.R/W, LCD1.LED-, Part1.GND, R2.leg2, R3.leg2
  VDD: LCD1.VDD, Part1.5V, R1.Pin_1, R2.leg1, R3.leg1
  N1: LCD1.V0, R3.wiper
  N2: LCD1.RS, Part1.D12/MISO
  N3: LCD1.E, Part1.D11_PWM/MOSI
  N4: LCD1.DB4, Part1.D5_PWM
  N5: LCD1.DB5, Part1.D4
  N6: LCD1.DB6, Part1.D3_PWM
  N7: LCD1.DB7, Part1.D2
  N8: LCD1.LED+, R1.Pin_0, R2.wiper
