# Fritzing sketch id224_led_ciclo_for_0 (saved by Fritzing 0.9.2b)
breadboards: 1

parts:
  LED1 = LED - 5mm [color="Red (633nm)" package="5 mm [THT]"]
  Componente1 = Arduino Uno (Rev3)
  LED2 = LED - 5mm [color="Green (570nm)" package="5 mm [THT]"]
  LED3 = LED - 5mm [color="Yellow (592nm)" package="5 mm [THT]"]
  Power_plug1 = Power plug

nets:
  GND: LED1.cathode, Componente1.GND, LED2.cathode, LED3.cathode, Power_plug1.GND
  N1: LED1.anode, Componente1.D13/SCK
  N2: Componente1.D11_PWM/MOSI, LED3.anode
  N3: Componente1.D12/MISO, LED2.anode
  5V: Componente1.5V, Power_plug1.VCC
