# Fritzing sketch id2250_Diagram_LCD_16x2__0 (saved by Fritzing 0.9.0b)
breadboards: 1

parts:
  Part1 = Arduino Uno (Rev3) - ICSP
  U1 = 74HC595 [package="DIP16 [THT]"]
  LCD1 = prefix0000_16x2_LCD_Turkey
  U2 = POT [package=alps_pot]

nets:
  N1: Part1.ICSP_MOSI, Part1.D11_PWM/MOSI, U1.DS
  N2: Part1.D10_PWM/SS, U1.ST_CP
  N3: Part1.D13/SCK, U1.SH_CP
  5V: Part1.5V, U1.MR, U1.VCC, LCD1.connector0, LCD1.connector3, U2.A
  GND: Part1.GND, U1.GND, U1.OE, LCD1.connector1, LCD1.connector2, LCD1.connector6, U2.E
  N4: U1.Q1, LCD1.connector5
  N5: U1.Q3, LCD1.connector7
  N6: U1.Q4, LCD1.connector12
  N7: U1.Q5, LCD1.connector13
  N8: U1.Q6, LCD1.connector14
  N9: U1.Q7, LCD1.connector15
  N10: LCD1.connector4, U2.S

notes:
  PIN ORDER
  DB7
  DB6
  DB5
  DB4
  DB3
  DB2
  DB1
  DB0
  E
  R/W
  RS
  V0
  VDD
  GND
  LED-
  LED+
  10K
