# Fritzing sketch id2251_LCD_con_74HC595_0 (saved by Fritzing 0.9.2b)
breadboards: 1

parts:
  Parte1 = Arduino Uno (Rev3)
  U2 = 74HC595 [package="DIP16 [THT]"]
  R1 = Resistor [tolerance=±5% resistance=220 package="2512 [SMD]"]
  U1 = LCD-16X2 [package=lcd-16x2]

nets:
  N1: Parte1.D9_PWM, U2.ST_CP
  N2: Parte1.D11_PWM/MOSI, U2.DS
  N3: Parte1.D13/SCK, U2.SH_CP
  5V: Parte1.5V, U2.MR, U2.VCC, R1.Pin_1, U1.VDD, U1.R_W, U1.K
  GND: Parte1.GND, U2.GND, U2.OE, U1.VSS, U1.VO
  N4: U2.Q1, U1.RS
  N5: U2.Q3, U1.E
  N6: U2.Q4, U1.DB4
  N7: U2.Q5, U1.DB5
  N8: U2.Q6, U1.DB6
  N9: U2.Q7, U1.DB7
  N10: R1.Pin_0, U1.A
