# Fritzing sketch id2252_LCDBCKLTCTRL_0 (saved by Fritzing 0.3.19b)
breadboards: 1

parts:
  LCD1 = LCD screen
  S1 = Toggle Switch [package=THT]
  VCC1 = obsolete Battery
  R1 = Rotary Potentiometer (Small)
  S2 = Toggle Switch [package=THT]

nets:
  N1: LCD1.LED+, S1.COM
  N2: LCD1.LED-, R1.leg1, S2.L2
  N3: S1.L2, VCC1.-
  N4: VCC1.+, S2.COM
  N5: R1.wiper, S2.L1

notes:
  LCD BACKLIGHT CONTROLLER
  Intensity-Full/Man. -Power
