# Fritzing sketch id2253_ton_lcd_0 (saved by Fritzing 0.9.2b)
breadboards: 1

parts:
  Componente1 = Arduino Mega ADK (Rev3)
  LCD1 = LCD screen

nets:
  GND: Componente1.GND, LCD1.VSS, LCD1.V0, LCD1.R/W, LCD1.LED-
  N1: Componente1.D12_PWM, LCD1.RS
  N2: Componente1.D11_PWM, LCD1.E
  5V: Componente1.5V, LCD1.VDD
  N3: Componente1.D2_PWM, LCD1.DB7
  N4: Componente1.D3_PWM, LCD1.DB6
  N5: Componente1.D4_PWM, LCD1.DB5
  N6: Componente1.D5_PWM, LCD1.DB4
  N7: Componente1.D7_PWM, LCD1.LED+
