# Fritzing sketch id2254_LCD_Placa_0 (saved by Fritzing 0.8.5b)
circuit board: 8.46667cm x 5.64444cm
breadboards: 1

parts:
  Componente1 = Arduino Uno (Rev3)
  LCD1 = LCD screen
  J1 = Infrared Proximity Sensor
  R1 = Rotary Potentiometer (Small) [maximum_resistance=100kΩ package=THT]

nets:
  N1: Componente1.D11_PWM/MOSI, LCD1.E
  N2: Componente1.D12/MISO, LCD1.RS
  GND: Componente1.GND, LCD1.VSS, LCD1.R/W, LCD1.LED-, J1.GND, R1.leg2
  N3: Componente1.D2, LCD1.DB7
  N4: Componente1.D3_PWM, LCD1.DB6
  N5: Componente1.D4, LCD1.DB5
  N6: Componente1.D5_PWM, LCD1.DB4
  N7: Componente1.D6_PWM, J1.Vout
  5V: Componente1.5V, LCD1.VDD, LCD1.LED+, J1.Vcc, R1.leg1
  N8: LCD1.V0, R1.wiper

notes:
  Sensor IR Nao encontrado. Entao coloquei essa porra ai.
