# Fritzing sketch id2255_LCD_0 (saved by Fritzing 0.9.2b)
breadboards: 1

parts:
  Part1 = Arduino Uno (Rev3)
  U1 = LCD-16X2 [package=lcd-16x2_noholes]
  R1 = Resistor [tolerance=±5% resistance=1k package="0805 [SMD]"]

nets:
  N1: Part1.D11_PWM/MOSI, U1.E
  N2: Part1.D12/MISO, U1.RS
  N3: Part1.D2, U1.DB7
  N4: Part1.D3_PWM, U1.DB6
  N5: Part1.D4, U1.DB5
  N6: Part1.D5_PWM, U1.DB4
  5V: Part1.5V, U1.VDD, U1.A
  N7: Part1.GND, R1.Pin_0
  N8: U1.VSS, U1.VO, U1.R_W, U1.K, R1.Pin_1
