# Fritzing sketch id2258_lcd_sketch_0 (saved by Fritzing 0.9.2b)
breadboards: 1

parts:
  part = Raspberry Pi 2
  LCD1 = LCD screen
  DHT1 = DHT22_Humidity_and_Temperature_Sensor
  BMP1 = BMP085_Breakout
  4_7_k_-_10_k_ohm_resistor = Resistor [tolerance=±5% resistance=220 package="0402 [SMD]"]

nets:
  N1: part.3v3, DHT1.connector1, 4_7_k_-_10_k_ohm_resistor.Pin_0
  N2: part.GPIO2, BMP1.connector4
  N3: part.GPIO3, BMP1.connector3
  N4: part.GPIO4, DHT1.connector2, 4_7_k_-_10_k_ohm_resistor.Pin_1
  N5: part.GPIO11, LCD1.DB7
  N6: part.GPIO5, LCD1.DB6
  N7: part.GPIO6, LCD1.DB5
  N8: part.GPIO13, LCD1.DB4
  N9: part.GPIO19, LCD1.E
  N10: part.GPIO26, LCD1.RS
  GND: part.GPIO14, part.GND, LCD1.VSS, LCD1.V0, LCD1.R/W, LCD1.LED-, DHT1.connector4, BMP1.connector7
  5V: part.5V, LCD1.VDD, LCD1.LED+, BMP1.connector1

notes:
  4.7k -10k ohm
  resistor between signal and voltage in on DHT22
