# Fritzing sketch id2263_valigetta_2.0_0 (saved by Fritzing 0.9.3b)
breadboards: 1

parts:
  Master = atmega328 [package=dip]
  C1 = Ceramic Capacitor [capacitance=22pF package="100 mil [THT, multilayer]"]
  C2 = Ceramic Capacitor [capacitance=22pF package="100 mil [THT, multilayer]"]
  XTAL1 = Crystal [frequency="16 Mhz" package=THT]
  i2c_Display = male pin header, 4 pins [form="♂ (male)"]
  KeyPad_3x4 = male pin header, 7 pins [form="♂ (male)"]
  Piezzo = Piezo Speaker [part_number=MT12D02]
  Q1 = NPN-Transistor [part_number=BC337 package="TO92 [THT]"]
  7805_atmega = Voltage Regulator - 5V [package="DPak [SMD]"]
  C4 = Ceramic Capacitor [capacitance=0.33µF package="100 mil [THT, multilayer]"]
  C5 = Ceramic Capacitor [capacitance=0.1µF package="100 mil [THT, multilayer]"]
  D1 = Rectifier Diode [part_number=1N4001 package="300 mil [THT]"]
  R3 = Resistor [tolerance=±5% resistance=10k package="1206 [SMD]"]
  R2 = Resistor [tolerance=±5% resistance=10k package="1206 [SMD]"]
  R1 = Resistor [tolerance=±5% resistance=10k package="1206 [SMD]"]
  Slave = atmega328 [package=dip]
  C8 = Ceramic Capacitor [capacitance=22pF package="100 mil [THT, multilayer]"]
  C9 = Ceramic Capacitor [capacitance=22pF package="100 mil [THT, multilayer]"]
  XTAL2 = Crystal [frequency="16 Mhz" package=THT]
  R5 = Resistor [tolerance=±5% resistance=10k package="1206 [SMD]"]
  Battery = Screw terminal - 2 pins [package=THT]
  Relay_2 = RELAY-2 [package=relay-g5v]
  J1_i2c = female pin header, 4 pins [form="♀ (female)"]
  J2_i2c = female pin header, 4 pins [form="♀ (female)"]
  J3_i2c = female pin header, 4 pins [form="♀ (female)"]
  Q2 = NPN-Transistor [part_number=BC547 package="TO92 [THT]"]
  Relay_J2 = screw terminal, 3 pins
  D4 = Rectifier Diode [part_number=1N4007 package="Melf DO-213 AB [SMD]"]
  R8 = Resistor [tolerance=±5% resistance=4.7k package="1206 [SMD]"]
  R11 = Resistor [tolerance=±5% resistance=1k package="1206 [SMD]"]
  Relay_1 = RELAY-2 [package=relay-g5v]
  D5 = Rectifier Diode [part_number=1N4007 package="Melf DO-213 AB [SMD]"]
  Q3 = NPN-Transistor [part_number=BC547 package="TO92 [THT]"]
  R12 = Resistor [tolerance=±5% resistance=4.7k package="1206 [SMD]"]
  Relay_J1 = screw terminal, 3 pins
  R14 = Resistor [tolerance=±5% resistance=1k package="1206 [SMD]"]
  LED1 = smd LED [color="Red (633nm)" package="1206 [SMD]"]
  LED2 = smd LED [color="Red (633nm)" package="1206 [SMD]"]
  R21 = Resistor [tolerance=±5% resistance=10 package="1206 [SMD]"]
  R4 = Resistor [tolerance=±5% resistance=4.7k package="1206 [SMD]"]
  Reset_S2 = Pushbutton [package=THT]
  ISP_Display_Seg = male pin header, 7 pins [form="♂ (male)"]
  Reset_S1 = Pushbutton [package=THT]
  C12 = Ceramic Capacitor [capacitance=100nF voltage=10V package="1206 [SMD, multilayer]"]
  C14 = Ceramic Capacitor [capacitance=100nF voltage=10V package="1206 [SMD, multilayer]"]
  UP = Pushbutton [package="[THT]"]
  DOWN = Pushbutton [package="[THT]"]
  CLEAR = Pushbutton [package="[THT]"]
  SEL = Pushbutton [package="[THT]"]
  R22 = Resistor [tolerance=±5% resistance=10k package="1206 [SMD]"]
  R24 = Resistor [tolerance=±5% resistance=10k package="1206 [SMD]"]
  R25 = Resistor [tolerance=±5% resistance=10k package="1206 [SMD]"]
  R26 = Resistor [tolerance=±5% resistance=10k package="1206 [SMD]"]
  StepDown_5V = screw terminal, 3 pins
  R27 = Resistor [tolerance=±5% resistance=470 package="1206 [SMD]"]
  W2812b = screw terminal, 3 pins

nets:
  N1: Master.RESET, R1.Pin_0, Reset_S1.leg1, C14.0
  Rx master: Master.D0_(RX)
  Tx master: Master.D1_(TX)
  Col0: Master.D2, KeyPad_3x4.pin1
  Col1: Master.D3_(PWM), KeyPad_3x4.pin2
  Col2: Master.D4, KeyPad_3x4.pin3
  5V: Master.VCC, Master.AVCC, Master.AREF, 7805_atmega.output_voltage, C5.1, R3.Pin_1, R2.Pin_1, R1.Pin_1, Slave.VCC, Slave.AVCC, Slave.AREF, R5.Pin_1, R22.Pin_1, R24.Pin_1, R25.Pin_1, R26.Pin_1
  GND: Master.GND, C1.0, C2.0, i2c_Display.pin4, Q1.E, 7805_atmega.GND, C4.0, C5.0, Slave.GND, C8.0, C9.0, Battery.pin2, J1_i2c.pin4, J2_i2c.pin4, J3_i2c.pin4, Q2.E, Q3.E, Reset_S2.leg0, ISP_Display_Seg.pin1, Reset_S1.leg0, UP.Pin_1, UP.Pin_2, DOWN.Pin_1, DOWN.Pin_2, CLEAR.Pin_1, CLEAR.Pin_2, SEL.Pin_1, SEL.Pin_2, StepDown_5V.pin2, W2812b.pin3
  N2: Master.XLAT1, C1.1, XTAL1.pin_1
  N3: Master.XLAT2, C2.1, XTAL1.pin_0
  UP: Master.D5_(PWM), UP.Pin_3, UP.Pin_4, R22.Pin_0
  DOWN: Master.D6_(PWM), DOWN.Pin_3, DOWN.Pin_4, R25.Pin_0
  CLEAR: Master.D7, CLEAR.Pin_3, R24.Pin_0
  SEL: Master.D8, SEL.Pin_3, R26.Pin_0
  N4: Master.D9_(PWM), R4.Pin_0
  SS: Master.D10_(PWM), ISP_Display_Seg.pin7
  MOSI: Master.D11_(PWM), ISP_Display_Seg.pin6
  MISO: Master.D12, ISP_Display_Seg.pin3
  SCK: Master.D13, ISP_Display_Seg.pin4
  Row3: Master.A0, KeyPad_3x4.pin7
  Row2: Master.A1, KeyPad_3x4.pin6
  Row1: Master.A2, KeyPad_3x4.pin5
  Row0: Master.A3, KeyPad_3x4.pin4
  SDA: Master.A4, i2c_Display.pin2, R3.Pin_0, Slave.A4, J1_i2c.pin2, J2_i2c.pin2, J3_i2c.pin2
  SCL: Master.A5, i2c_Display.pin1, R2.Pin_0, Slave.A5, J1_i2c.pin1, J2_i2c.pin1, J3_i2c.pin1
  5V Scondary: i2c_Display.pin3, Relay_2.2, J1_i2c.pin3, J2_i2c.pin3, J3_i2c.pin3, D4.cathode, R11.Pin_1, Relay_1.2, D5.cathode, R14.Pin_1, R21.Pin_1, ISP_Display_Seg.pin2, StepDown_5V.pin3, W2812b.pin1
  N5: Piezzo.pin1, Q1.C
  N6: Piezzo.pin2, R21.Pin_0
  N7: Q1.B, R4.Pin_1
  N8: 7805_atmega.input_voltage, C4.1, D1.cathode
  Battery: D1.anode, Battery.pin1, StepDown_5V.pin1
  N9: Slave.RESET, R5.Pin_0, Reset_S2.leg1, C12.0
  Rx slave: Slave.D0_(RX)
  Tx slave: Slave.D1_(TX)
  Led1_rosso: Slave.D3_(PWM)
  N10: Slave.XLAT1, C8.1, XTAL2.pin_1
  N11: Slave.XLAT2, C9.1, XTAL2.pin_0
  Led1_blu: Slave.D5_(PWM)
  Led1_verde: Slave.D6_(PWM)
  Led: Slave.D11_(PWM), R27.Pin_0
  Relay 2: Slave.D12, R8.Pin_0
  Relay 1: Slave.D13, R12.Pin_0
  N12: Relay_2.1, Relay_J2.pin1
  N13: Relay_2.5, Relay_2.6, Relay_J2.pin2
  N14: Relay_2.9, Q2.C, D4.anode, LED2.cathode
  N15: Relay_2.10, Relay_J2.pin3
  N16: Q2.B, R8.Pin_1
  N17: R11.Pin_0, LED2.anode
  N18: Relay_1.1, Relay_J1.pin1
  N19: Relay_1.5, Relay_1.6, Relay_J1.pin2
  N20: Relay_1.9, D5.anode, Q3.C, LED1.cathode
  N21: Relay_1.10, Relay_J1.pin3
  N22: Q3.B, R12.Pin_1
  N23: R14.Pin_0, LED1.anode
  Reset master: ISP_Display_Seg.pin5
  DTR slave: C12.1
  DTR Master: C14.1
  N24: R27.Pin_1, W2812b.pin2
