# Fritzing sketch id2264_lcd_mp3_0 (saved by Fritzing 0.9.1b)
circuit board: 8.46667cm x 5.64444cm
breadboards: 1

parts:
  play_00 = Pushbutton [package="[THT]"]
  LCD1 = LCD screen
  Raspberry_Pi1 = Raspberry Pi B+
  prev_01 = Pushbutton [package="[THT]"]
  R1 = Trimmer Potentiometer [maximum_resistance=10kΩ package=THT]
  next_02 = Pushbutton [package="[THT]"]
  info_5 = Pushbutton [package="[THT]"]
  quit_7 = Pushbutton [package="[THT]"]

nets:
  N1: play_00.Pin_1, play_00.Pin_2, Raspberry_Pi1.GPIO17
  VSS: play_00.Pin_3, play_00.Pin_4, LCD1.VSS, LCD1.R/W, LCD1.LED-, Raspberry_Pi1.GND, prev_01.Pin_3, prev_01.Pin_4, R1.leg1, next_02.Pin_3, next_02.Pin_4, info_5.Pin_3, info_5.Pin_4, quit_7.Pin_3, quit_7.Pin_4
  VDD: LCD1.VDD, LCD1.LED+, Raspberry_Pi1.3v3, R1.leg2
  N2: LCD1.V0, R1.wiper
  N3: LCD1.RS, Raspberry_Pi1.GPIO22
  N4: LCD1.E, Raspberry_Pi1.GPIO11
  N5: LCD1.DB4, Raspberry_Pi1.GPIO23
  N6: LCD1.DB5, Raspberry_Pi1.GPIO10
  N7: LCD1.DB6, Raspberry_Pi1.GPIO9
  N8: LCD1.DB7, Raspberry_Pi1.GPIO25
  N9: Raspberry_Pi1.GPIO4, quit_7.Pin_1, quit_7.Pin_2
  N10: Raspberry_Pi1.GPIO27, next_02.Pin_1, next_02.Pin_2
  N11: Raspberry_Pi1.GPIO24, info_5.Pin_1, info_5.Pin_2
  N12: Raspberry_Pi1.GPIO18, prev_01.Pin_1, prev_01.Pin_2
