# Fritzing sketch id2266_LCD_Nokia_5110+Sensor_DS18B20_0 (saved by Fritzing 0.9.2b)
breadboards: 1

parts:
  Componente1 = Arduino Uno (Rev3)
  Nokia_5110_LCD_Module1 = Nokia5110LCDModule
  R1 = Resistor [tolerance=±5% resistance=4.7k package="0603 [SMD]"]
  U1 = TEMPERATURE-SENSOR [package=to-92]

nets:
  N1: Componente1.D8, Nokia_5110_LCD_Module1.connector6
  N2: Componente1.D9_PWM, Nokia_5110_LCD_Module1.connector5
  N3: Componente1.D10_PWM/SS, Nokia_5110_LCD_Module1.connector4
  N4: Componente1.D11_PWM/MOSI, Nokia_5110_LCD_Module1.connector3
  N5: Componente1.D12/MISO, Nokia_5110_LCD_Module1.connector2
  GND: Componente1.GND, Nokia_5110_LCD_Module1.connector1, U1.GND
  N6: Componente1.D7, R1.Pin_0, U1.ADJ
  N7: Componente1.3V3, Nokia_5110_LCD_Module1.connector0, Nokia_5110_LCD_Module1.connector7
  5V: Componente1.5V, R1.Pin_1, U1.VCC

notes:
  Ligação do LCD Nokia 5110 e Sensor DS18B20.
  Deve-se utilizar um resistor 4K7 entre os pino de dados e vcc do sensor.
