# Fritzing sketch id2268_LCD_Pong_Circuit_0 (saved by Fritzing 0.9.1b)
breadboards: 1

parts:
  Part1 = Arduino Uno (Rev3)
  U1 = LCD-16X2 [package=lcd-16x2_noholes]
  R1 = Rotary Potentiometer (Small) [maximum_resistance=100kΩ package=THT]
  LED1 = LED - 5mm [color="Red (633nm)" package="5 mm [THT]"]
  LED2 = LED - 5mm [color="Red (633nm)" package="5 mm [THT]"]
  LED3 = LED - 5mm [color="Red (633nm)" package="5 mm [THT]"]
  R2 = Resistor [tolerance=±5% resistance=220 package=THT]
  R3 = Resistor [tolerance=±5% resistance=220 package=THT]
  R4 = Resistor [tolerance=±5% resistance=220 package=THT]
  R5 = Rotary Potentiometer (Small) [maximum_resistance=100kΩ package=THT]
  J1 = Piezo Speaker
  S1 = Pushbutton [package="[THT]"]
  R6 = Resistor [tolerance=±5% resistance=10k package=THT]

nets:
  N1: Part1.A0, R5.wiper
  N2: Part1.D8, R4.Pin_0
  N3: Part1.D9_PWM, S1.Pin_1, S1.Pin_2, R6.Pin_0
  N4: Part1.D10_PWM/SS, J1.pin2
  N5: Part1.D11_PWM/MOSI, U1.E
  N6: Part1.D12/MISO, U1.RS
  GND: Part1.GND, U1.VSS, U1.R_W, U1.K, LED1.cathode, LED2.cathode, LED3.cathode, R5.leg1, J1.pin1, R6.Pin_1
  N7: Part1.D2, U1.DB7
  N8: Part1.D3_PWM, U1.DB6
  N9: Part1.D4, U1.DB5
  N10: Part1.D5_PWM, U1.DB4
  N11: Part1.D6_PWM, R2.Pin_0
  N12: Part1.D7, R3.Pin_0
  5V: Part1.5V, U1.VDD, U1.A, R5.leg2, S1.Pin_3, S1.Pin_4
  N13: U1.VO, R1.wiper
  N14: LED1.anode, R2.Pin_1
  N15: LED2.anode, R3.Pin_1
  N16: LED3.anode, R4.Pin_1
