# Fritzing sketch id2269_lcd_powertip_pc2004c_20x4_0 (saved by Fritzing 0.7.0b)
breadboards: 1

parts:
  LCD1 = LCD screen
  Arduino1 = Arduino
  R1 = Trimmer Potentiometer [maximum_resistance=10kΩ package=THT]

nets:
  VSS: LCD1.VSS, LCD1.V0, LCD1.R/W, LCD1.LED-, Arduino1.GND
  VDD: LCD1.VDD, Arduino1.+5V, R1.leg1, R1.leg2
  N1: LCD1.RS, Arduino1.D7
  N2: LCD1.E, Arduino1.D8
  N3: LCD1.DB4, Arduino1.D9
  N4: LCD1.DB5, Arduino1.D10
  N5: LCD1.DB6, Arduino1.D11
  N6: LCD1.DB7, Arduino1.D12
  N7: LCD1.LED+, R1.wiper

notes:
  Powertip LCD pc2004c
  20x4 (distinto al dibujo)
  LiquidCrystal lcd(7, 8, 9, 10, 11, 12);
  Tek
