# Fritzing sketch id226_acender_LED_0 (saved by Fritzing 0.8.7b)
circuit board: 8.46667cm x 5.64444cm
breadboards: 1

parts:
  Componente1 = Arduino Uno (Rev3)
  R1 = Resistor [tolerance=±5% resistance=330 package=THT]
  LED1 = LED - 5mm [color="Red (633nm)" package="5 mm [THT]"]

nets:
  N1: Componente1.D13/SCK, R1.Pin_1
  N2: Componente1.GND, LED1.cathode
  N3: R1.Pin_0, LED1.anode

notes:
  * o resistor deve ser ligado ao terminal positivo do LED
  * o jumper do pino 13 do arduino deve ser ligado ao resistor
  * o jumper do pino GND do arduino deve ser ligado ao terminal negativo do LED
