# Fritzing sketch id2270_LCd_connection_0 (saved by Fritzing 0.9.3b)
breadboards: 1

parts:
  Part1 = Arduino Mega ADK (Rev3)
  LCD1 = LCD screen
  R1 = Rotary Potentiometer (Small) [maximum_resistance=10kΩ package=THT]

nets:
  N1: Part1.5V, LCD1.V0
  GND: Part1.GND, LCD1.VSS, LCD1.R/W, LCD1.LED-, R1.wiper, R1.leg2
  N2: Part1.D32, LCD1.DB7
  N3: Part1.D33, LCD1.DB6
  N4: Part1.D34, LCD1.DB5
  N5: Part1.D35, LCD1.DB4
  N6: Part1.D36, LCD1.RS
  N7: Part1.D37, LCD1.E
  N8: LCD1.VDD, LCD1.LED+, R1.leg1
