# Fritzing sketch id2271_LCDTest_0 (saved by Fritzing 0.9.1b)
circuit board: 8.46667cm x 5.64444cm
breadboards: 1

parts:
  パーツ1 = Arduino Uno (Rev3)
  R2 = Trimmer Potentiometer [maximum_resistance=10kΩ package=THT]
  R1 = Resistor [tolerance=±5% resistance=270 package=THT]
  LCD1 = SD1602VBWB-XA-G-G

nets:
  N1: パーツ1.D8, LCD1.connector11
  N2: パーツ1.D12/MISO, LCD1.connector12
  N3: パーツ1.D13/SCK, LCD1.connector13
  N4: パーツ1.D2, LCD1.connector3
  N5: パーツ1.D4, LCD1.connector5
  N6: パーツ1.D7, LCD1.connector10
  N7: パーツ1.5V, R2.leg2, R1.Pin_0, LCD1.connector1
  N8: パーツ1.GND, R2.leg1, LCD1.connector0, LCD1.connector4, LCD1.connector15
  N9: R2.wiper, LCD1.connector2
  N10: R1.Pin_1, LCD1.connector14
