# Fritzing sketch id2273_LockP4_0 (saved by Fritzing 0.9.3b)
circuit board: 18.0606cm x 7.3181cm
breadboards: 1

parts:
  Motion_Sensor = PIR_sensor
  Screen = adafruit [part_number="Adafruit #714 and #716"]
  Lock = Basic Servo
  Billie_the_buzzer = Piezo Speaker
  Arduino = Arduino Mega 2560 (Rev3)

nets:
  VCC: Motion_Sensor.connector1, Screen.connector80, Lock.vcc, Arduino.5V
  N1: Motion_Sensor.connector2, Arduino.D33
  GND: Motion_Sensor.connector3, Screen.connector102, Screen.connector103, Screen.connector104, Lock.gnd, Billie_the_buzzer.pin1, Arduino.GND
  N2: Screen.connector79, Arduino.3V3
  N3: Screen.connector81, Arduino.A0
  N4: Screen.connector82, Arduino.A1
  N5: Screen.connector83, Arduino.A2
  N6: Screen.connector84, Arduino.A3
  N7: Screen.connector85, Screen.connector107, Arduino.A4, Arduino.SDA
  N8: Screen.connector86, Screen.connector106, Arduino.A5, Arduino.D21/SCL, Arduino.SCL
  N9: Screen.connector87, Arduino.AREF
  N10: Screen.connector88, Arduino.D0_RX0
  N11: Screen.connector89, Arduino.D1_TX0
  N12: Screen.connector90, Arduino.D2_PWM
  N13: Screen.connector91, Arduino.D3_PWM
  N14: Screen.connector92, Arduino.D4_PWM
  N15: Screen.connector93, Arduino.D5_PWM
  N16: Screen.connector94, Arduino.D6_PWM
  N17: Screen.connector95, Arduino.D7_PWM
  N18: Screen.connector96, Arduino.D8_PWM
  N19: Screen.connector97, Arduino.D9_PWM
  N20: Screen.connector98, Arduino.D10_PWM
  N21: Screen.connector99, Arduino.D11_PWM
  N22: Screen.connector100, Arduino.D12_PWM
  N23: Screen.connector101, Arduino.D13_PWM
  N24: Screen.connector105, Arduino.RESET
  N25: Screen.connector108, Arduino.VIN
  N26: Lock.pulse, Arduino.D29
  N27: Billie_the_buzzer.pin2, Arduino.D27

notes:
  PIR 33
  Servo 29
  Buzzer 25
  A little experiment. Non-functional and buggy. I don't reccomend you use this, and I highly discourage Fabricacting it.
