# Fritzing sketch id2274_LCDTaunt_0 (saved by Fritzing 0.9.2b)
circuit board: 12.2369cm x 8.3186cm
breadboards: 1

parts:
  TTP223B1 = richardbruneau00000
  LCD1 = LCD screen
  R1 = Rotary Potentiometer (Small) [maximum_resistance=10kΩ package=THT]
  R2 = Resistor [tolerance=±5% resistance=10k package=THT]
  Part1 = Arduino Uno (Rev3)

nets:
  VSS: TTP223B1.connector8, LCD1.VSS, LCD1.R/W, LCD1.LED-, R1.leg1, Part1.GND
  VDD: TTP223B1.connector9, LCD1.VDD, R1.leg2, R2.Pin_0, Part1.5V
  N1: TTP223B1.connector10, Part1.D7
  N2: LCD1.V0, R1.wiper
  N3: LCD1.RS, Part1.D12/MISO
  N4: LCD1.E, Part1.D11_PWM/MOSI
  N5: LCD1.DB4, Part1.D5_PWM
  N6: LCD1.DB5, Part1.D4
  N7: LCD1.DB6, Part1.D3_PWM
  N8: LCD1.DB7, Part1.D2
  N9: LCD1.LED+, R2.Pin_1
