# Fritzing sketch id2275_Thermometer_Project.fz_0 (saved by Fritzing 0.9.2b)
circuit board: 22.8712cm x 10.087cm
breadboards: 1

parts:
  LCD1 = LCD screen
  Part1 = Arduino Uno (Rev3)
  Part2 = Variable Capacitor [capacitance=100nF max_capacitance=10pF min_capacitance=2pF voltage=35V]
  T1 = LM35 Temperature Sensor [package="TO92 [THT]"]
  R1 = Resistor [tolerance=±5% resistance=220 package=THT]

nets:
  GND: LCD1.VSS, LCD1.R/W, Part1.GND, Part2.2, T1.GND, R1.Pin_0
  VDD: LCD1.VDD, LCD1.LED+, Part1.5V, Part2.1, T1.+Vs
  N1: LCD1.V0, Part2.0
  N2: LCD1.RS, Part1.D7
  N3: LCD1.E, Part1.D8
  N4: LCD1.DB4, Part1.D9_PWM
  N5: LCD1.DB5, Part1.D10_PWM/SS
  N6: LCD1.DB6, Part1.D11_PWM/MOSI
  N7: LCD1.DB7, Part1.D12/MISO
  N8: LCD1.LED-, R1.Pin_1
  N9: Part1.A1, T1.Vout
