# Fritzing sketch id2277_LCD_ultrasound_fritzing_0 (saved by Fritzing 0.9.3b)
breadboards: 1

parts:
  부품1 = Arduino Uno (Rev3)
  hc-sr1 = hc-sr04
  LCD1 = LCD screen
  R1 = Rotary Potentiometer (Small) [maximum_resistance=100kΩ package=THT]

nets:
  N1: 부품1.D8, LCD1.DB6
  N2: 부품1.D9_PWM, LCD1.DB5
  N3: 부품1.D10_PWM/SS, LCD1.DB4
  N4: 부품1.D11_PWM/MOSI, LCD1.E
  N5: 부품1.D12/MISO, LCD1.RS
  N6: 부품1.D5_PWM, hc-sr1.Echo
  N7: 부품1.D6_PWM, hc-sr1.Trig
  N8: 부품1.D7, LCD1.DB7
  5V: 부품1.5V, hc-sr1.VCC, LCD1.VDD, LCD1.LED+, R1.leg1
  GND: 부품1.GND, hc-sr1.GND, LCD1.VSS, LCD1.R/W, LCD1.LED-, R1.leg2
  N9: LCD1.V0, R1.wiper
