# Fritzing sketch id2279_LCD_with_KeyPad_on_Arduino_UNO_0 (saved by Fritzing 0.9.2b)

parts:
  Parte1 = Arduino Uno (Rev3)
  Matrix_keypad1 = CMG
  U1 = LCD-16X2 [package=lcd-16x2]
  R1 = Resistor [tolerance=±5% resistance=220 package="1206 [SMD]"]

nets:
  N1: Parte1.A0, Matrix_keypad1.connector31
  N2: Parte1.A1, Matrix_keypad1.connector32
  N3: Parte1.D8, Matrix_keypad1.connector25
  N4: Parte1.D9_PWM, Matrix_keypad1.connector26
  N5: Parte1.D10_PWM/SS, Matrix_keypad1.connector27
  N6: Parte1.D11_PWM/MOSI, Matrix_keypad1.connector28
  N7: Parte1.D12/MISO, Matrix_keypad1.connector29
  N8: Parte1.D13/SCK, Matrix_keypad1.connector30
  N9: Parte1.D2, U1.DB7
  N10: Parte1.D3_PWM, U1.DB6
  N11: Parte1.D4, U1.DB5
  N12: Parte1.D5_PWM, U1.DB4
  N13: Parte1.D6_PWM, U1.E
  N14: Parte1.D7, U1.RS
  5V: Parte1.5V, U1.VDD, R1.Pin_0
  GND: Parte1.GND, U1.VSS, U1.VO, U1.R_W, U1.K
  N15: U1.A, R1.Pin_1

notes:
  danielriveraayala@gmail.com
