# Fritzing sketch id227_ACIDBEAT_0 (saved by Fritzing 0.9.3b)
circuit board: 15.0367cm x 8.01483cm
breadboards: 1

parts:
  ATMEGA_328P-PU = atmega328 [package=dip]
  POWER_12V = Power plug
  REG_5V = Voltage Regulator - 5V [package="TO220 [THT]"]
  N_CHANEL_MOSFET = Basic FET N-Channel [part_number=IRFZ4N package="TO220 [THT]"]
  R1 = Resistor [tolerance=±5% resistance=1k package=THT]
  R2 = Resistor [tolerance=±5% resistance=1k package=THT]
  R3 = Resistor [tolerance=±5% resistance=1k package=THT]
  R4 = Resistor [tolerance=±5% resistance=10k package=THT]
  10uf = Electrolytic Capacitor [capacitance=10µF package="100 mil [THT, electrolytic]"]
  10uf_2 = Electrolytic Capacitor [capacitance=10µF package="100 mil [THT, electrolytic]"]
  D1 = Rectifier Diode [part_number=1N4001 package="300 mil [THT]"]
  CLAP-D2 = RCA [package=rca_lock]
  HITHATO-D3 = RCA [package=rca_lock]
  HITHATC-D4 = RCA [package=rca_lock]
  HITON-D5 = RCA [package=rca_lock]
  LOWTON-D6 = RCA [package=rca_lock]
  SNARE-D7 = RCA [package=rca_lock]
  KICK-D8 = RCA [package=rca_lock]
  Q2 = Basic FET N-Channel [part_number=IRFZ4N package="TO220 [THT]"]
  Q3 = Basic FET N-Channel [part_number=IRFZ4N package="TO220 [THT]"]
  Q4 = Basic FET N-Channel [part_number=IRFZ4N package="TO220 [THT]"]
  Q5 = Basic FET N-Channel [part_number=IRFZ4N package="TO220 [THT]"]
  Q6 = Basic FET N-Channel [part_number=IRFZ4N package="TO220 [THT]"]
  Q7 = Basic FET N-Channel [part_number=IRFZ4N package="TO220 [THT]"]
  MIDI_IN = AUDIO-JACK2 [package=audio-jack]
  ON/OFF = SWITCH-DPDT [package=eg2211]
  ICSP = female pin header, 6 pins [form="♀ (female)"]
  CRYSTAL = Crystal [frequency="16 Mhz" package=THT]
  22pf = Ceramic Capacitor [capacitance=22pF package="100 mil [THT, multilayer]"]
  22pf_2 = Ceramic Capacitor [capacitance=22pF package="100 mil [THT, multilayer]"]
  R5 = Resistor [tolerance=±5% resistance=10k package=THT]
  R6 = Resistor [tolerance=±5% resistance=10k package=THT]
  R7 = Resistor [tolerance=±5% resistance=1k package=THT]
  R8 = Resistor [tolerance=±5% resistance=10k package=THT]
  R9 = Resistor [tolerance=±5% resistance=1k package=THT]
  R10 = Resistor [tolerance=±5% resistance=10k package=THT]
  R11 = Resistor [tolerance=±5% resistance=1k package=THT]
  R12 = Resistor [tolerance=±5% resistance=1k package=THT]
  R13 = Resistor [tolerance=±5% resistance=10k package=THT]
  R14 = Resistor [tolerance=±5% resistance=10k package=THT]
  6N36 = IC, DIP package, 8 pins [chip_label=6N36 part_number=OPTOCOPLADOR]
  MIDI_/_ICSP = SWITCH-DPDT [package=eg2211]
  R15 = Resistor [tolerance=±5% resistance=220 package=THT]
  LED1 = LED - 5mm [color="Red (633nm)" package="5 mm [THT]"]
  LED2 = LED - 5mm [color="Red (633nm)" package="5 mm [THT]"]
  R16 = Resistor [tolerance=±5% resistance=220 package=THT]
  R17 = Resistor [tolerance=±5% resistance=220 package=THT]
  LED3 = LED - 5mm [color="Red (633nm)" package="5 mm [THT]"]
  LED4 = LED - 5mm [color="Red (633nm)" package="5 mm [THT]"]
  R18 = Resistor [tolerance=±5% resistance=220 package=THT]
  LED5 = LED - 5mm [color="Red (633nm)" package="5 mm [THT]"]
  R19 = Resistor [tolerance=±5% resistance=220 package=THT]
  LED6 = LED - 5mm [color="Red (633nm)" package="5 mm [THT]"]
  R20 = Resistor [tolerance=±5% resistance=220 package=THT]
  LED7 = LED - 5mm [color="Red (633nm)" package="5 mm [THT]"]
  R21 = Resistor [tolerance=±5% resistance=220 package=THT]
  R22 = Resistor [tolerance=±5% resistance=10k package=THT]
  R23 = Resistor [tolerance=±5% resistance=10k package=THT]
  R24 = Resistor [tolerance=±5% resistance=220 package=THT]
  2N3904 = NPN-Transistor [package="TO92 [THT]"]
  D2 = Rectifier Diode [part_number=1N4001 package="300 mil [THT]"]
  R25 = Resistor [tolerance=±5% resistance=470 package=THT]
  BREAK_OUT = double row male pin header, 10 pins [form="♂ (male)"]
  CLOCK_OUT = AUDIO-JACK2 [package=audio-jack]
  CLOCK_OUT/2 = AUDIO-JACK2 [package=audio-jack]
  MIDI_OUT = AUDIO-JACK2 [package=audio-jack]
  R26 = Resistor [tolerance=±5% resistance=220 package=THT]
  R27 = Resistor [tolerance=±5% resistance=220 package=THT]
  R28 = Resistor [tolerance=±5% resistance=220 package=THT]
  LED8 = LED - 3mm [color="Red (633nm)" package="3 mm [THT]"]
  R29 = Resistor [tolerance=±5% resistance=220 package=THT]
  LED9 = LED - 3mm [color="Red (633nm)" package="3 mm [THT]"]

nets:
  N1: ATMEGA_328P-PU.RESET, ICSP.pin3, R22.Pin_0
  N2: ATMEGA_328P-PU.D0_(RX), MIDI_/_ICSP.2, MIDI_/_ICSP.1, MIDI_/_ICSP.4, MIDI_/_ICSP.5
  N3: ATMEGA_328P-PU.D1_(TX), R27.Pin_0
  N4: ATMEGA_328P-PU.D2, R12.Pin_1, LED7.anode
  N5: ATMEGA_328P-PU.D3_(PWM), R11.Pin_1, LED6.anode
  N6: ATMEGA_328P-PU.D4, R9.Pin_1, LED5.anode
  N7: ATMEGA_328P-PU.VCC, ATMEGA_328P-PU.AVCC, ATMEGA_328P-PU.AREF, REG_5V.output_voltage, 10uf_2.+, ICSP.pin1, 6N36.pin6, 6N36.pin8, R22.Pin_1, R25.Pin_0, BREAK_OUT.pin6
  GND: ATMEGA_328P-PU.GND, POWER_12V.GND, REG_5V.GND, N_CHANEL_MOSFET.source, R4.Pin_0, 10uf.-, 10uf_2.-, Q2.source, Q3.source, Q4.source, Q5.source, Q6.source, Q7.source, MIDI_IN.SLEEVE, ICSP.pin2, 22pf.1, 22pf_2.0, R5.Pin_0, R6.Pin_0, R8.Pin_0, R10.Pin_0, R13.Pin_0, R14.Pin_0, R15.Pin_0, R16.Pin_1, R17.Pin_0, R18.Pin_0, R19.Pin_0, R20.Pin_0, R21.Pin_0, R23.Pin_1, 2N3904.E, BREAK_OUT.pin5, CLOCK_OUT.SLEEVE, CLOCK_OUT/2.SLEEVE, MIDI_OUT.SLEEVE, R26.Pin_0, R28.Pin_0, R29.Pin_1
  N8: ATMEGA_328P-PU.XLAT1, CRYSTAL.pin_1, 22pf.0
  N9: ATMEGA_328P-PU.XLAT2, CRYSTAL.pin_0, 22pf_2.1
  N10: ATMEGA_328P-PU.D5_(PWM), R7.Pin_1, LED4.anode
  N11: ATMEGA_328P-PU.D6_(PWM), R1.Pin_1, LED3.anode
  N12: ATMEGA_328P-PU.D7, R2.Pin_1, LED2.anode
  N13: ATMEGA_328P-PU.D8, R3.Pin_1, LED1.anode
  N14: ATMEGA_328P-PU.D9_(PWM), CLOCK_OUT.RING, CLOCK_OUT.RSH, CLOCK_OUT.TIP, CLOCK_OUT.TSH, LED8.anode
  N15: ATMEGA_328P-PU.D10_(PWM), CLOCK_OUT/2.RING, CLOCK_OUT/2.RSH, CLOCK_OUT/2.TIP, CLOCK_OUT/2.TSH, LED9.anode
  N16: ATMEGA_328P-PU.D11_(PWM), ICSP.pin6
  N17: ATMEGA_328P-PU.D12, ICSP.pin5, BREAK_OUT.pin7
  N18: ATMEGA_328P-PU.D13, ICSP.pin4, BREAK_OUT.pin8
  N19: ATMEGA_328P-PU.A0, BREAK_OUT.pin4
  N20: ATMEGA_328P-PU.A1, BREAK_OUT.pin3
  N21: ATMEGA_328P-PU.A2, BREAK_OUT.pin2
  N22: ATMEGA_328P-PU.A3, BREAK_OUT.pin1
  N23: ATMEGA_328P-PU.A4, BREAK_OUT.pin10
  N24: ATMEGA_328P-PU.A5, BREAK_OUT.pin9
  N25: POWER_12V.VCC, D1.anode, CLAP-D2.PIN, CLAP-D2.SWITCH, HITHATO-D3.PIN, HITHATO-D3.SWITCH, HITHATC-D4.PIN, HITHATC-D4.SWITCH, HITON-D5.PIN, HITON-D5.SWITCH, LOWTON-D6.PIN, LOWTON-D6.SWITCH, SNARE-D7.PIN, SNARE-D7.SWITCH, KICK-D8.PIN, KICK-D8.SWITCH
  N26: REG_5V.input_voltage, 10uf.+, ON/OFF.3, ON/OFF.6
  N27: N_CHANEL_MOSFET.gate, R3.Pin_0, R4.Pin_1
  N28: N_CHANEL_MOSFET.drain, KICK-D8.SHELL
  N29: R1.Pin_0, Q3.gate, R6.Pin_1
  N30: R2.Pin_0, Q2.gate, R5.Pin_1
  N31: D1.cathode, ON/OFF.2, ON/OFF.1, ON/OFF.4, ON/OFF.5
  N32: CLAP-D2.SHELL, Q7.drain
  N33: HITHATO-D3.SHELL, Q6.drain
  N34: HITHATC-D4.SHELL, Q5.drain
  N35: HITON-D5.SHELL, Q4.drain
  N36: LOWTON-D6.SHELL, Q3.drain
  N37: SNARE-D7.SHELL, Q2.drain
  N38: Q4.gate, R7.Pin_0, R8.Pin_1
  N39: Q5.gate, R9.Pin_0, R10.Pin_1
  N40: Q6.gate, R11.Pin_0, R13.Pin_1
  N41: Q7.gate, R12.Pin_0, R14.Pin_1
  N42: MIDI_IN.RING, MIDI_IN.RSH, 6N36.pin3, D2.anode
  N43: MIDI_IN.TIP, MIDI_IN.TSH, R24.Pin_0
  N44: 6N36.pin2, R24.Pin_1, D2.cathode
  N45: 6N36.pin5, R23.Pin_0, 2N3904.B
  N46: MIDI_/_ICSP.3, MIDI_/_ICSP.6, 2N3904.C, R25.Pin_1
  N47: R15.Pin_1, LED1.cathode
  N48: LED2.cathode, R16.Pin_0
  N49: R17.Pin_1, LED3.cathode
  N50: LED4.cathode, R18.Pin_1
  N51: LED5.cathode, R19.Pin_1
  N52: LED6.cathode, R20.Pin_1
  N53: LED7.cathode, R21.Pin_1
  N54: MIDI_OUT.RING, MIDI_OUT.RSH, R27.Pin_1
  N55: MIDI_OUT.TIP, MIDI_OUT.TSH, R26.Pin_1
  N56: R28.Pin_1, LED8.cathode
  N57: R29.Pin_0, LED9.cathode

notes:
  13
  12
  11
  A5
  RST
  GND
  VCC
  A4
  A3
  A2
  A1
  A0
  D12
  D13
  NCHANEL MOSFETS
  EXPAND! & PLAY!
  VOLCA BEAT
  LED STRIP
  CONTROLLER
  FABRICAMARCIANA.WORDPRESS.COM
