# Fritzing sketch id2280_metboard_0 (saved by Fritzing 0.7.10b)
breadboards: 1

parts:
  U1 = atmega328 [package=dip]
  S1 = Pushbutton [package="[THT]"]
  XTAL1 = Crystal [package=THT]
  R1 = Resistor [tolerance=±5% resistance=220 package=THT]
  C4 = Ceramic Disk Capacitor [package=THT]
  C5 = Ceramic Capacitor [package=THT]
  C6 = Ceramic Capacitor [package=THT]
  CONN1 = USB connector [package=THT]
  D1 = Zener Diode [part_number=1N4732A breakdown_voltage=3.6V package="Melf DO-213 AB [SMD]"]
  D2 = Zener Diode [part_number=1N4732A breakdown_voltage=3.6V package="Melf DO-213 AB [SMD]"]
  R2 = Resistor [tolerance=±5% resistance=1.5k package=THT]
  R3 = Resistor [tolerance=±5% resistance=1M package=THT]
  R4 = Resistor [tolerance=±5% resistance=68 package=THT]
  R5 = Resistor [tolerance=±5% resistance=68 package=THT]
  C7 = Electrolytic Capacitor [package=THT]  # not connected

nets:
  N1: U1.RESET, S1.Pin_3, S1.Pin_4, R1.Pin_0
  N2: U1.D2, R4.Pin_0
  N3: U1.D4, R5.Pin_0
  VCC: U1.VCC, U1.AVCC, U1.AREF, R1.Pin_1, C6.pin_0, CONN1.5V
  GND: U1.GND, U1.D7, S1.Pin_1, S1.Pin_2, C4.pin_1, C5.pin_0, C6.pin_1, CONN1.GND, CONN1.chassis5, CONN1.chassis6, D1.cathode, D2.cathode, R2.Pin_0, R3.Pin_0
  N4: U1.XLAT1, XTAL1.pin_0, C5.pin_1
  N5: U1.XLAT2, XTAL1.pin_1, C4.pin_0
  N6: CONN1.d-, D1.anode, R2.Pin_1, R5.Pin_1
  N7: CONN1.d+, D2.anode, R3.Pin_1, R4.Pin_1

notes:
  0.1uF
  22pF
  220Ω
  1.5kΩ, 3v6,1MΩ, 3v6
  Yellow wire d+,
  Grey wire d-
  68Ω,68Ω, 10uF
  Orange Wire- Jumper to start Bootloader (Pin 13)
  MetBoard v1
  Based on
  V-USB ASPloader
  +5V
  GND
  GND
  +5V
