# Fritzing sketch id2281_LCDuinopico_0 (saved by Fritzing 0.9.0b)
breadboards: 1

parts:
  LCD1 = LCD screen
  LED1 = LED - 5mm [color="Red (633nm)" package="5 mm [THT]"]
  U1 = atmega328 [package=dip]
  S1 = Toggle Switch [package=THT]
  U2 = Voltage Regulator - 5V [package="TO220 [THT]"]
  VCC1 = Battery block 9V
  C3 = Ceramic Capacitor [capacitance=10nF package="100 mil [THT, multilayer]"]
  C2 = Ceramic Capacitor [capacitance=100nF package="100 mil [THT, multilayer]"]
  R1 = Resistor [tolerance=±5% resistance=2.2k package=THT]

nets (from the schematic view):
  GND: LCD1.VSS, LCD1.R/W, LED1.cathode, U1.GND, U2.GND, VCC1.-, C3.0, C2.1
  VDD: LCD1.VDD, LED1.anode, U1.VCC, U1.AVCC, U2.output_voltage, C3.1, R1.Pin_1
  N1: LCD1.V0, R1.Pin_0
  N2: LCD1.RS, U1.D12
  N3: LCD1.E, U1.D11_(PWM)
  N4: LCD1.DB4, U1.D2
  N5: LCD1.DB5, U1.D3_(PWM)
  N6: LCD1.DB6, U1.D4
  N7: LCD1.DB7, U1.XLAT1
  N8: S1.COM, VCC1.+
  N9: S1.L2, U2.input_voltage, C2.0
