# Fritzing sketch id2284_LDD_Board_4_0 (saved by Fritzing 0.9.3b)
circuit board: 9.12742cm x 8.52624cm

parts:
  LDD-1000H1 = ldd-mh
  LDD-1000H4 = ldd-mh
  LDD-1000H2 = ldd-mh
  U1 = RJ45 Jack [package=rj45-8]
  C2 = Capacitor [package=cap-pth-small2]
  U2 = Voltage Regulator [package=to220-adj]
  LDD-1000H5 = ldd-mh
  LDD-1000H3 = ldd-mh
  C1 = Capacitor [package=cap-pth-small2]
  J6 = screw terminal, 3 pins
  J5 = screw terminal, 3 pins
  J3 = screw terminal, 3 pins
  J1 = screw terminal, 3 pins
  J7 = screw terminal, 3 pins

nets:
  GND: LDD-1000H1.connector0, LDD-1000H1.connector1, LDD-1000H4.connector0, LDD-1000H4.connector1, LDD-1000H2.connector0, LDD-1000H2.connector1, U1.2, U1.3, U1.5, C2.2, U2.ADJ, LDD-1000H5.connector0, LDD-1000H5.connector1, LDD-1000H3.connector0, LDD-1000H3.connector1, C1.1, J6.pin3
  12V: LDD-1000H1.connector2, LDD-1000H1.connector3, LDD-1000H4.connector2, LDD-1000H4.connector3, LDD-1000H2.connector2, LDD-1000H2.connector3, U2.IN, LDD-1000H5.connector2, LDD-1000H5.connector3, LDD-1000H3.connector2, LDD-1000H3.connector3, C1.2, J6.pin1
  N1: LDD-1000H1.connector4, U1.7
  N2: LDD-1000H1.connector25, LDD-1000H1.connector26
  N3: LDD-1000H1.connector27, LDD-1000H1.connector28, J1.pin2
  N4: LDD-1000H4.connector4, U1.8
  N5: LDD-1000H4.connector25, LDD-1000H4.connector26, J5.pin3
  N6: LDD-1000H4.connector27, LDD-1000H4.connector28, J3.pin1
  N7: LDD-1000H2.connector4, U1.4
  N8: LDD-1000H2.connector25, LDD-1000H2.connector26, J7.pin1
  N9: LDD-1000H2.connector27, LDD-1000H2.connector28, J7.pin2
  N10: U1.1, LDD-1000H5.connector4
  N11: U1.6, LDD-1000H3.connector4
  N12: C2.1, U2.OUT, J6.pin2
  N13: LDD-1000H5.connector25, LDD-1000H5.connector26, J5.pin1
  N14: LDD-1000H5.connector27, LDD-1000H5.connector28, J5.pin2
  N15: LDD-1000H3.connector25, LDD-1000H3.connector26, J3.pin2
  N16: LDD-1000H3.connector27, LDD-1000H3.connector28, J3.pin3
