# Fritzing sketch id2285_Alarm_with_LDR_0 (saved by Fritzing 0.9.0b)
breadboards: 1

parts:
  LED1 = LED - 5mm [color="Red (633nm)" package="5 mm [THT]"]
  J1 = Piezo Speaker
  R1 = Resistor [tolerance=±5% resistance=10k package=THT]
  R2 = Photocell (LDR) [package=THT]
  Part1 = Arduino Uno (Rev3)
  R3 = Resistor [tolerance=±5% resistance=220 package=THT]
  R4 = Resistor [tolerance=±5% resistance=100 package=THT]
  LED2 = LED - 5mm [color="Red (633nm)" package="5 mm [THT]"]
  LED3 = LED - 5mm [color="Red (633nm)" package="5 mm [THT]"]
  R5 = Resistor [tolerance=±5% resistance=220 package=THT]
  R6 = Resistor [tolerance=±5% resistance=220 package=THT]

nets:
  N1: LED1.anode, J1.pin1, R1.Pin_0, Part1.GND, R3.Pin_0, LED2.cathode, LED3.anode, R5.Pin_0
  N2: J1.pin2, R4.Pin_0
  N3: R1.Pin_1, R2.pin_0, Part1.A0
  N4: R2.pin_1, Part1.5V
  N5: Part1.D2, R3.Pin_1
  N6: Part1.D3_PWM, R5.Pin_1
  N7: Part1.D4, R6.Pin_1
  N8: Part1.D5_PWM, R4.Pin_1
  N9: LED2.anode, R6.Pin_0

notes:
  Components REQD.:
  1) Arduino UNO
  2) Solderless Breadboard
  3) Buzzer 5V [x1]
  4) LDR [x1]
  5) Resitor 10kOhm [x1]
  6) Resistor 100Ohm [x1]
  7) Resistor 220Ohm [x3]
  8) LED [x3]
  9) Jumper Wires
