# Fritzing sketch id2286_LDR_Datalogger_0 (saved by Fritzing 0.7.7b)
breadboards: 1

parts:
  Arduino1 = Arduino
  J1 = female pin header, 6 pins [form="♀ (female)"]
  R1 = Photocell (LDR) [package=THT]
  R2 = Resistor [tolerance=±5% resistance=1k package=THT]

nets:
  N1: Arduino1.GND, J1.pin5, R2.Pin_1
  N2: Arduino1.D13, J1.pin2
  N3: Arduino1.D12, J1.pin4
  N4: Arduino1.D11, J1.pin3
  N5: Arduino1.D10, J1.pin1
  N6: Arduino1.3V3, J1.pin6
  N7: Arduino1.+5V, R1.pin_0
  N8: Arduino1.A0, R1.pin_1, R2.Pin_0

notes:
  3.3V - 3.3V
  gnd - gnd
  MISO - Pin 12
  MOSI - Pin 11
  CLK - Pin 13
  CS - Pin 10
