# Fritzing sketch id2287_ac_bulb_fritzing_0 (saved by Fritzing 0.8.7b)
breadboards: 1

parts:
  Part1 = Arduino Uno (Rev3)
  R1 = Resistor [tolerance=±5% resistance=220 package=THT]
  K1 = Relay [part_number=FRS1B-S package=THT]
  Q1 = NPN-Transistor [package="TO92 [THT]"]
  R2 = Resistor [tolerance=±5% resistance=220 package=THT]
  AC_Socket = Header 2 [package=screwterminal-3.5mm-2_lock]
  Lamp = Header 2 [package=screwterminal-3.5mm-2_lock]
  R3 = Photocell (LDR) [package=THT]

nets:
  N1: Part1.A0, R1.Pin_1, R3.pin_0
  N2: Part1.D13/SCK, R2.Pin_0
  N3: Part1.5V, R1.Pin_0, K1.COIL2
  N4: Part1.GND, Q1.E, R3.pin_1
  N5: K1.COIL1, Q1.C
  N6: K1.C1, K1.C2, AC_Socket.1
  N7: K1.B, Lamp.1
  N8: Q1.B, R2.Pin_1
  N9: AC_Socket.2, Lamp.2
