# Fritzing sketch id2288_Laser_Security_System_Using_LDR_(Photocell)_0 (saved by Fritzing 0.9.1b)
breadboards: 1

parts:
  Q1 = NPN-Transistor [package="TO92 [THT]"]
  R1 = Photocell (LDR) [package=THT]
  R2 = Resistor [tolerance=±5% resistance=10k package=THT]
  LED1 = LED - 5mm [color="Red (633nm)" package="5 mm [THT]"]
  VCC1 = 4 x AAA Battery Mount

nets:
  N1: Q1.E, R1.pin_0, VCC1.-
  N2: Q1.B, R1.pin_1, R2.Pin_0
  N3: Q1.C, LED1.cathode
  N4: R2.Pin_1, LED1.anode, VCC1.+
