# Fritzing sketch id2289_diagram_0 (saved by Fritzing 0.9.3b)
breadboards: 1

parts:
  LED1 = LED - 5mm [color="Red (633nm)" package="5 mm [THT]"]
  R1 = Resistor [tolerance=±5% resistance=220 package=THT]
  LED2 = LED - 5mm [color="Red (633nm)" package="5 mm [THT]"]
  R2 = Resistor [tolerance=±5% resistance=220 package=THT]
  Part1 = Arduino Uno (Rev3)
  R3 = Photocell (LDR) [package=THT]
  R4 = Resistor [tolerance=±5% resistance=220 package="0805 [SMD]"]

nets:
  N1: LED1.cathode, R1.Pin_1
  N2: LED1.anode, Part1.D7
  N3: R1.Pin_0, R2.Pin_0, Part1.GND, R4.Pin_1
  N4: LED2.cathode, R2.Pin_1
  N5: LED2.anode, Part1.D3_PWM
  N6: Part1.A0, R3.pin_1, R4.Pin_0
  N7: Part1.5V, R3.pin_0
