# Fritzing sketch id228_servos_0 (saved by Fritzing 0.7.0b)

parts:
  Arduino1 = Arduino
  J1 = Basic Servo
  J2 = Basic Servo

nets:
  N1: Arduino1.D8, J2.pulse
  N2: Arduino1.D7, J1.pulse
  VCC: Arduino1.+5V, J1.vcc, J2.vcc
  GND: Arduino1.GND, J1.gnd, J2.gnd
