# Fritzing sketch id2290_LDR_Simples_0 (saved by Fritzing 0.9.3b)
breadboards: 1

parts:
  Componente1 = Arduino Uno (Rev3)
  R1 = Photocell (LDR) [package=THT]
  R2 = Resistor [tolerance=±5% resistance=1k package="2512 [SMD]"]
  LED1 = smd LED [color="Red (633nm)" package="0805 [SMD]"]
  LED2 = smd LED [color="Green (555nm)" package="0805 [SMD]"]
  R3 = Resistor [tolerance=±5% resistance=330 package="2512 [SMD]"]
  R4 = Resistor [tolerance=±5% resistance=330 package="2512 [SMD]"]

nets:
  N1: Componente1.A0, R1.pin_0, R2.Pin_0
  N2: Componente1.GND, R2.Pin_1, LED1.cathode, LED2.cathode
  N3: Componente1.D1/TX, R3.Pin_0
  N4: Componente1.D2, R4.Pin_0
  N5: Componente1.5V, R1.pin_1
  N6: LED1.anode, R3.Pin_1
  N7: LED2.anode, R4.Pin_1
