# Fritzing sketch id2291_LDR_R&G_0 (saved by Fritzing 0.9.3b)
breadboards: 1

parts:
  Part1 = Arduino Mega ADK (Rev3)
  R1 = Photocell (LDR) [package=THT]
  LED1 = LED - 5mm [color="Red (633nm)" package="5 mm [THT]"]
  LED2 = LED - 5mm [color="Red (633nm)" package="5 mm [THT]"]
  R2 = Resistor [tolerance=±5% resistance=220 package="2512 [SMD]"]
  R3 = Resistor [tolerance=±5% resistance=220 package="0603 [SMD]"]
  R4 = Resistor [tolerance=±5% resistance=220 package="2512 [SMD]"]

nets:
  N1: Part1.A0, R1.pin_1, R4.Pin_0
  N2: Part1.GND, LED1.cathode, LED2.cathode, R4.Pin_1
  N3: Part1.D9_PWM, R3.Pin_1
  N4: Part1.D8_PWM, R2.Pin_0
  N5: Part1.5V, R1.pin_0
  N6: LED1.anode, R3.Pin_0
  N7: LED2.anode, R2.Pin_1
