# Fritzing sketch id2292_shiftregister_0 (saved by Fritzing 0.9.2b)
breadboards: 1

parts:
  Part1 = Arduino Uno (Rev3)
  R1 = Resistor [tolerance=±5% resistance=2k package=THT]
  R2 = Resistor [tolerance=±5% resistance=2k package=THT]
  ldr = Photocell (LDR) [package=THT]

nets:
  N1: Part1.A0, R2.Pin_1, ldr.pin_0
  N2: Part1.GND, R2.Pin_0
  N3: Part1.AREF, R1.Pin_0, ldr.pin_1
  N4: Part1.5V, R1.Pin_1
