# Fritzing sketch id2293_lecteur_rfid_0 (saved by Fritzing 0.9.2b)
breadboards: 1

parts:
  LCD1 = LCD screen  # not connected
  Eleman3 = RFID-RC522
  Composant3 = Arduino Uno (Rev3)
  U1 = POT [package=pot_mammoth]

nets:
  N1: Eleman3.connector8, Composant3.D10_PWM/SS
  N2: Eleman3.connector9, Composant3.D13/SCK
  N3: Eleman3.connector10, Composant3.D11_PWM/MOSI
  N4: Eleman3.connector11, Composant3.D12/MISO
  N5: Eleman3.connector13, Composant3.GND, U1.E
  N6: Eleman3.connector14, Composant3.D9_PWM
  N7: Eleman3.connector15, Composant3.3V3
  N8: Composant3.5V, U1.S
