# Fritzing sketch id2295_weather_led_0 (saved by Fritzing 0.9.3b)
breadboards: 1

parts:
  Raspberry_Pi1 = Raspberry Pi B+
  R1 = Resistor [tolerance=±5% resistance=220 package=THT]
  LED1 = RGB LED (com. cathode, rgb) [package="5 mm [THT]"]

nets:
  N1: Raspberry_Pi1.GPIO22, R1.Pin_0
  N2: Raspberry_Pi1.GPIO24, LED1.blue_anode
  N3: Raspberry_Pi1.GPIO23, LED1.green_anode
  N4: Raspberry_Pi1.GND, LED1.common_cathode
  N5: R1.Pin_1, LED1.red_anode
