# Fritzing sketch id2298_james_4N35_wsWK2iM_0 (saved by Fritzing 0.9.3b)
circuit board: 2.43787cm x 2.58084cm
breadboards: 1

parts:
  part = Optocoupler [package=THT]
  Switch = Pushbutton [package="[THT]"]
  Battry = Battery
  part_2 = LED - 5mm [color="Red (633nm)" package="5 mm [THT]"]

nets:
  N1: part.Pin_1, Battry.+, part_2.anode
  N2: part.Pin_2, Switch.Pin_1, Switch.Pin_2
  N3: part.Pin_5, part_2.cathode
  N4: Switch.Pin_3, Switch.Pin_4, Battry.-

notes:
  4N35
  LED
  James Tech
