# Fritzing sketch id2299_ClockmatrixSound_0 (saved by Fritzing 0.9.3b)
breadboards: 1

parts:
  WeMos_D1_Mini1 = WeMos D1 Mini
  DFRobot_DFPlayer_Mini1 = DFRobot DFPlayer Mini [part_number=DFR0299]
  Part1 = LED Matrix - Serial Interface - Red/Green/Blue
  SP1 = SPEAKER [package=pcb_mount_speaker]
  R2 = TRIMPOT [package=3386u]
  R3 = Resistor [tolerance=±5% resistance=220 package="2512 [SMD]"]
  Part2 = LED Matrix - Serial Interface - Red/Green/Blue  # not connected
  Part3 = LED Matrix - Serial Interface - Red/Green/Blue  # not connected
  Part4 = LED Matrix - Serial Interface - Red/Green/Blue  # not connected
  J1 = Power Jack [package=power_jack_smd]  # not connected
  X1 = USB Connectors [package=usb-minib]  # not connected

nets:
  VCC: WeMos_D1_Mini1.5V, DFRobot_DFPlayer_Mini1.VCC, Part1.VCC, R2.CCW
  N1: WeMos_D1_Mini1.A0, R2.WIPER
  N2: WeMos_D1_Mini1.D3, Part1.MISO
  N3: WeMos_D1_Mini1.D5, Part1.GND
  N4: WeMos_D1_Mini1.D7, Part1.CS
  N5: WeMos_D1_Mini1.G, DFRobot_DFPlayer_Mini1.GND-1, DFRobot_DFPlayer_Mini1.GND-2, Part1.SCK, R2.CW
  N6: DFRobot_DFPlayer_Mini1.SPK_1, SP1.-
  N7: DFRobot_DFPlayer_Mini1.SPK_2, SP1.+
  N8: DFRobot_DFPlayer_Mini1.BUSY, R3.Pin_1

notes:
  1000 Ohm Resistor between
  Tx to Busy
  10 K ( 10.000 ) Ohm
  Pot resistor, or potentiometer.
  A0 to middle pot pin, and pin1,3,Vcc, Grnd
  8 Ohm speaker
  Made by WannaDuino of The Real LiVe
  visit for builds, projects,coupons for Banggood and other cool stuff and videos, www.wannaduino.com or,
  www.youtube.com/cc/WannaDuinoTheRealLive
  5V 2 A
  4x4 8x8 Led matrix
  Vcc to 5V
  Grnd to Ground
  Din toD7
  Cs to D3
  Clk to D5
  www.wannaduino.com
