# Fritzing sketch id229_Arduino_Acrylic_LED_0 (saved by Fritzing 0.9.2b)
circuit board: 8.89939cm x 3.93138cm
breadboards: 1

parts:
  Part1 = Arduino Nano (Rev3.0)
  LED1 = RGB LED (com. cathode, rgb) [package="5 mm [THT]"]
  LED2 = RGB LED (com. cathode, rgb) [package="5 mm [THT]"]
  LED3 = RGB LED (com. cathode, rgb) [package="5 mm [THT]"]
  LED4 = RGB LED (com. cathode, rgb) [package="5 mm [THT]"]
  LED5 = RGB LED (com. cathode, rgb) [package="5 mm [THT]"]
  S1 = Pushbutton [package="[THT]"]
  R5 = Resistor [tolerance=±5% resistance=220 package=THT]
  R6 = Resistor [tolerance=±5% resistance=220 package=THT]
  R7 = Resistor [tolerance=±5% resistance=220 package=THT]
  R8 = Resistor [tolerance=±5% resistance=220 package=THT]
  R9 = Resistor [tolerance=±5% resistance=220 package=THT]
  R10 = Resistor [tolerance=±5% resistance=220 package=THT]
  R11 = Resistor [tolerance=±5% resistance=220 package=THT]
  R12 = Resistor [tolerance=±5% resistance=220 package=THT]
  R13 = Resistor [tolerance=±5% resistance=220 package=THT]
  R14 = Resistor [tolerance=±5% resistance=220 package=THT]
  R16 = Resistor [tolerance=±5% resistance=220 package=THT]
  R17 = Resistor [tolerance=±5% resistance=220 package=THT]
  R18 = Resistor [tolerance=±5% resistance=220 package=THT]
  R19 = Resistor [tolerance=±5% resistance=220 package=THT]
  R20 = Resistor [tolerance=±5% resistance=220 package=THT]
  R21 = Resistor [tolerance=±5% resistance=220 package=THT]
  R22 = Resistor [tolerance=±5% resistance=220 package=THT]
  R23 = Resistor [tolerance=±5% resistance=220 package=THT]

nets:
  N1: Part1.GND, LED1.common_cathode, LED2.common_cathode, LED3.common_cathode, LED4.common_cathode, LED5.common_cathode, R14.Pin_0, R16.Pin_0
  N2: Part1.D2, R20.Pin_1
  N3: Part1.D3, R13.Pin_1
  N4: Part1.D4, R9.Pin_1
  N5: Part1.D5, R12.Pin_1
  N6: Part1.D6, R11.Pin_1
  N7: Part1.D7, R8.Pin_1
  N8: Part1.D8, R10.Pin_1
  N9: Part1.D9, R7.Pin_1
  N10: Part1.D10, R6.Pin_1
  N11: Part1.D11/MOSI, R5.Pin_1
  N12: Part1.D12/MISO, R17.Pin_1
  N13: Part1.5V, S1.Pin_3, S1.Pin_4, R23.Pin_1
  N14: Part1.A4, S1.Pin_1, S1.Pin_2, R14.Pin_1
  N15: Part1.A3, R22.Pin_1
  N16: Part1.A2, R21.Pin_1
  N17: Part1.A1, R18.Pin_1
  N18: Part1.A0, R16.Pin_1, R23.Pin_0
  N19: Part1.D13/SCK, R19.Pin_1
  N20: LED1.red_anode, R22.Pin_0
  N21: LED1.green_anode, R21.Pin_0
  N22: LED1.blue_anode, R20.Pin_0
  N23: LED2.red_anode, R11.Pin_0
  N24: LED2.green_anode, R12.Pin_0
  N25: LED2.blue_anode, R13.Pin_0
  N26: LED3.red_anode, R9.Pin_0
  N27: LED3.green_anode, R8.Pin_0
  N28: LED3.blue_anode, R10.Pin_0
  N29: LED4.red_anode, R7.Pin_0
  N30: LED4.green_anode, R5.Pin_0
  N31: LED4.blue_anode, R6.Pin_0
  N32: LED5.red_anode, R17.Pin_0
  N33: LED5.green_anode, R18.Pin_0
  N34: LED5.blue_anode, R19.Pin_0

notes:
  B
  A3
  A2
  D2
  D6
  D3
  D5
  D7
  D4
  D8
  D11
  D10
  D9
  A1
  D13
  D12
  2ND LEG = GND
  LEDS:
  470Ω
  LDR
  10KΩ
  470Ωx9
  USB SIDE
  +
  -
  Looney May '16
  VER 1.0
  AcryLED
  IF YOU CAN READ THIS, YOUR ETCHING IS GOD-LIKE
