# Fritzing sketch id22_FUZZFACEONELAYER_0 (saved by Fritzing 0.8.7b)
circuit board: 5.3cm x 3.78cm
breadboards: 1

parts:
  R2 = Resistor [tolerance=±5% resistance=220 package=THT]
  C1 = Electrolytic Capacitor [capacitance=1µF package="100 mil [THT, electrolytic]"]
  Q1 = NPN-Transistor [package="TO92 [THT]"]
  C2 = Ceramic Capacitor [capacitance=100nF package="100 mil [THT, multilayer]"]
  TRS2 = Audio Jack (TRS) 3.5mm [package="PG203J [THT]"]
  R4 = Resistor [tolerance=±5% resistance=220 package=THT]
  R7 = Resistor [tolerance=±5% resistance=220 package=THT]
  Q2 = NPN-Transistor [package="TO92 [THT]"]
  TRS1 = Audio Jack (TRS) 3.5mm [package="4Ucon 08780 [THT]"]
  C3 = Electrolytic Capacitor [capacitance=1µF package="100 mil [THT, electrolytic]"]
  R5 = Trimmer Potentiometer [maximum_resistance=10kΩ package=THT]
  R6 = Trimmer Potentiometer [maximum_resistance=10kΩ package=THT]
  Power_plug1 = Power plug
  R3 = Resistor [tolerance=±5% resistance=220 package=THT]

nets:
  N1: R2.Pin_0, Q1.C, Q2.B
  N2: R2.Pin_1, Power_plug1.VCC, R3.Pin_0
  N3: C1.-, TRS2.Tip
  N4: C1.+, Q1.B, R7.Pin_0
  GND: Q1.E, TRS2.Sleeve, TRS1.Sleeve, C3.-, R5.leg1, R6.leg1, Power_plug1.GND
  N5: C2.0, C2.1, R4.Pin_1, R6.leg2, R3.Pin_1
  N6: R4.Pin_0, Q2.C
  N7: R7.Pin_1, Q2.E, R5.leg2
  N8: TRS1.Ring, R6.wiper
  N9: C3.+, R5.wiper
