# Fritzing sketch id2300_Ultrasonic_0 (saved by Fritzing 0.9.3b)
breadboards: 1

parts:
  hc-sr1 = hc-sr04
  Componente1 = Arduino Uno (Rev3) - ICSP

nets:
  VCC: hc-sr1.VCC, Componente1.5V
  N1: hc-sr1.Trig, Componente1.ICSP_MISO, Componente1.D12/MISO
  N2: hc-sr1.Echo, Componente1.D13/SCK
  GND: hc-sr1.GND, Componente1.GND
