# Fritzing sketch id2302_LED_Basic_0 (saved by Fritzing 0.9.2b)
circuit board: 1.5cm x 4cm
breadboards: 1

parts:
  LED1 = LED - 5mm [color="Red (633nm)" package="5 mm [THT]"]
  Part1 = Arduino Uno (Rev3)
  R1 = Resistor [tolerance=±5% resistance=330 package=THT]

nets:
  N1: LED1.cathode, Part1.GND
  N2: LED1.anode, R1.Pin_0
  N3: Part1.D13/SCK, R1.Pin_1
