# Fritzing sketch id2303_Led_Blink_0 (saved by Fritzing 0.9.2b)
breadboards: 1

parts:
  R1 = Resistor [tolerance=±5% resistance=220 package=THT]
  LED1 = LED - 5mm [color="Red (633nm)" package="5 mm [THT]"]
  Part1 = Arduino Uno (Rev3)  # not connected

nets:
  N1: R1.Pin_1, LED1.cathode
