# Fritzing sketch id2304_LED_Blink_fritzing_0 (saved by Fritzing 0.9.3b)

parts:
  부품1 = Arduino Uno (Rev3)
  LED1 = smd LED [color="Red (633nm)" package="1206 [SMD]"]

nets:
  N1: 부품1.D13/SCK, LED1.anode
  N2: 부품1.GND, LED1.cathode
