# Fritzing sketch id2307_adjustable_delays_fritzing_0 (saved by Fritzing 0.8.7b)
breadboards: 1

parts:
  Part1 = Arduino Uno (Rev3)
  R1 = Resistor [tolerance=±5% resistance=220 package=THT]
  R2 = Resistor [tolerance=±5% resistance=220 package=THT]
  S1 = Pushbutton [package="[THT]"]
  R4 = Resistor [tolerance=±5% resistance=220 package=THT]
  S2 = Pushbutton [package="[THT]"]
  R5 = Resistor [tolerance=±5% resistance=220 package=THT]
  LED3 = LED - 5mm [color="Red (633nm)" package="5 mm [THT]"]
  LED4 = LED - 5mm [color="Red (633nm)" package="5 mm [THT]"]

nets:
  N1: Part1.D12/MISO, R2.Pin_0
  N2: Part1.D13/SCK, R1.Pin_0
  N3: Part1.D2, S1.Pin_3, S1.Pin_4, R4.Pin_1
  N4: Part1.D4, S2.Pin_3, S2.Pin_4, R5.Pin_1
  N5: Part1.5V, S1.Pin_1, S1.Pin_2, S2.Pin_1, S2.Pin_2
  N6: Part1.GND, R4.Pin_0, R5.Pin_0, LED3.cathode, LED4.cathode
  N7: R1.Pin_1, LED3.anode
  N8: R2.Pin_1, LED4.anode
