# Fritzing sketch id2310_trsiletimde_led_yanar_0 (saved by Fritzing 0.9.2b)
breadboards: 1

parts:
  R1 = Resistor [tolerance=±5% resistance=100k package=THT]
  R2 = Resistor [tolerance=±5% resistance=330 package=THT]
  R3 = Resistor [tolerance=±5% resistance=10k package=THT]
  Q1 = NPN-Transistor [part_number=bc237 package="SOT-23 [SMD]"]
  LED1 = LED - 3mm [color="Red (633nm)" package="3 mm [THT]"]
  R4 = Resistor [tolerance=±5% resistance=470 package=THT]
  S1 = Round Pushbutton
  VCC1 = 4 x AAA Battery Mount

nets:
  N1: R1.Pin_0, S1.leg1
  N2: R1.Pin_1, R4.Pin_1, VCC1.+
  N3: R2.Pin_0, R3.Pin_0, S1.leg0
  N4: R2.Pin_1, Q1.0
  N5: R3.Pin_1, Q1.2, VCC1.-
  N6: Q1.1, LED1.cathode
  N7: LED1.anode, R4.Pin_0
