# Fritzing sketch id2311_trsiletimde_led_yanar_q7tXzDq_0 (saved by Fritzing 0.9.2b)
breadboards: 1

parts:
  part = Resistor [tolerance=±5% resistance=10k package=THT]
  part_2 = Resistor [tolerance=±5% resistance=330 package=THT]
  part_3 = Resistor [tolerance=±5% resistance=10k package=THT]
  part_4 = NPN-Transistor [part_number=BC237 package="SOT-23 [SMD]"]
  part_5 = LED - 3mm [color="Red (633nm)" package="3 mm [THT]"]
  S1 = Round Pushbutton
  VCC1 = 4 x AAA Battery Mount
  R5 = Resistor [tolerance=±5% resistance=470 package=THT]  # not connected
  part_6 = Resistor [tolerance=±5% resistance=470 package=THT]

nets:
  N1: part.Pin_0, S1.leg1
  N2: part.Pin_1, VCC1.+, part_6.Pin_1
  N3: part_2.Pin_0, part_3.Pin_0, S1.leg0
  N4: part_2.Pin_1, part_4.0
  N5: part_3.Pin_1, part_4.2, VCC1.-
  N6: part_4.1, part_5.cathode
  N7: part_5.anode, part_6.Pin_0
