# Fritzing sketch id2312_LED_circuit_skematic_0 (saved by Fritzing 0.9.2b)
breadboards: 1

parts:
  LED1 = smd LED [color="White (8000K)" package="0603 [SMD]"]
  LED2 = smd LED [color="White (8000K)" package="0603 [SMD]"]
  LED3 = smd LED [color="White (8000K)" package="0603 [SMD]"]
  LED4 = smd LED [color="White (8000K)" package="0603 [SMD]"]
  LED5 = smd LED [color="White (8000K)" package="0603 [SMD]"]
  LED6 = smd LED [color="White (8000K)" package="0603 [SMD]"]
  LED7 = smd LED [color="White (8000K)" package="0603 [SMD]"]
  LED8 = smd LED [color="White (8000K)" package="0603 [SMD]"]
  LED9 = smd LED [color="White (8000K)" package="0603 [SMD]"]
  LED10 = smd LED [color="White (8000K)" package="0603 [SMD]"]
  LED11 = smd LED [color="White (8000K)" package="0603 [SMD]"]
  LED12 = smd LED [color="White (8000K)" package="0603 [SMD]"]
  R1 = Resistor [tolerance=±5% resistance=150 package=THT]
  R2 = Resistor [tolerance=±5% resistance=150 package=THT]
  R3 = Resistor [tolerance=±5% resistance=150 package=THT]
  R4 = Resistor [tolerance=±5% resistance=150 package=THT]
  R5 = Resistor [tolerance=±5% resistance=150 package=THT]
  R6 = Resistor [tolerance=±5% resistance=150 package=THT]
  R7 = Resistor [tolerance=±5% resistance=150 package=THT]
  R8 = Resistor [tolerance=±5% resistance=150 package=THT]
  R9 = Resistor [tolerance=±5% resistance=150 package=THT]
  R10 = Resistor [tolerance=±5% resistance=150 package=THT]
  R11 = Resistor [tolerance=±5% resistance=150 package=THT]
  R12 = Resistor [tolerance=±5% resistance=150 package=THT]
  R13 = Resistor [tolerance=±10% resistance=1k package=THT]
  U1 = 555 Timer [package="SO8 [SMD]"]
  C1 = Ceramic Capacitor [capacitance=10nF package="100 mil [THT, multilayer]"]
  C2 = Ceramic Capacitor [capacitance=100nF package="100 mil [THT, multilayer]"]
  R14 = Rotary Potentiometer (Small) [maximum_resistance=100kΩ package=THT]
  D1 = Diode [package=diode-1n4001]
  D2 = Diode [package=diode-1n4001]
  R15 = Resistor [tolerance=±5% resistance=1k package=THT]

nets:
  N1: LED1.cathode, LED12.cathode
  N2: LED1.anode, R1.Pin_1
  N3: LED2.anode, R2.Pin_1
  N4: LED3.anode, R3.Pin_1
  N5: LED4.anode, R4.Pin_1
  N6: LED5.anode, R5.Pin_1
  N7: LED6.anode, R6.Pin_1
  N8: LED7.anode, R7.Pin_1
  N9: LED8.anode, R8.Pin_1
  N10: LED9.anode, R9.Pin_1
  N11: LED10.anode, R10.Pin_1
  N12: LED11.anode, R11.Pin_1
  N13: LED12.anode, R12.Pin_1
  N14: R1.Pin_0, R12.Pin_0
  GND: R13.Pin_1, U1.Pin_1, C1.0, C2.0
  N15: U1.Pin_4, U1.Pin_8
  N16: U1.Pin_5, C1.1
  N17: U1.Pin_7, D1.C, D2.A, R15.Pin_0
  N18: R14.leg1, D2.C
  N19: R14.leg2, D1.A
