# Fritzing sketch id2313_LED_e_2_Botoes_0 (saved by Fritzing 0.8.6b)
breadboards: 1

parts:
  S1 = Pushbutton [package="[THT]"]
  S2 = Pushbutton [package="[THT]"]
  R1 = Resistor [tolerance=±5% resistance=220 package=THT]
  R2 = Resistor [tolerance=±5% resistance=220 package=THT]
  Componente1 = Arduino Uno (Rev3)
  LED1 = LED - 5mm [color="Red (633nm)" package="5 mm [THT]"]
  R3 = Resistor [tolerance=±5% resistance=220 package=THT]

nets:
  N1: S1.Pin_1, S1.Pin_2, S2.Pin_1, S2.Pin_2, Componente1.5V
  N2: S1.Pin_3, S1.Pin_4, R2.Pin_1, Componente1.D3_PWM
  N3: S2.Pin_3, S2.Pin_4, R1.Pin_1, Componente1.D2
  N4: R1.Pin_0, R2.Pin_0, Componente1.GND, R3.Pin_0
  N5: Componente1.D12/MISO, LED1.anode
  N6: LED1.cathode, R3.Pin_1
