# Fritzing sketch id2314_Led_0 (saved by Fritzing 0.9.2b)
circuit board: 8.46667cm x 5.64444cm
breadboards: 1

parts:
  Parte1 = Arduino Uno (Rev3)
  S1 = Pushbutton [package="[THT]"]
  R1 = Resistor [tolerance=±5% resistance=220 package=THT]
  LED1 = LED - 5mm [color="Red (633nm)" package="5 mm [THT]"]

nets:
  N1: Parte1.5V, R1.Pin_1
  N2: Parte1.GND, LED1.cathode
  N3: S1.Pin_1, S1.Pin_2, LED1.anode
  N4: S1.Pin_3, S1.Pin_4, R1.Pin_0
