# Fritzing sketch id2315_LED230VAC_0 (saved by Fritzing 0.9.2b)

parts:
  LED1 = LED - 5mm [color="Green (570nm)" package="5 mm [THT]"]
  R1 = Resistor [tolerance=±5% resistance=47k package=THT]
  D1 = Rectifier Diode [part_number=1N4007 package="300 mil [THT]"]

nets:
  N1: LED1.cathode, R1.Pin_1
  N2: LED1.anode, D1.cathode

notes:
  Señalizar enchufe con LED conectado a 230V Alterna
  Circuito muy util para señalizar que una toma de corriente o enchufe al que se hade conectar un aparato que funciona a 230 VAC, tiene tensión y está en servicio.
  Precauciones.-
  Hay que tener en cuenta que es un circuito cuyas partes vivas están sometidas a 230 VAC y que por lo tanto es una tensión peligrosa para el cuerpo humano. Tened cuidado cuando hagais pruebas.
  Hay que tener en cuenta que el diodo LED y el 1N4007 van conectados en serie, es decir, el cátodo de uno se suelda al ánodo del otro, si no se hace así no funciona.
  Más información aquí:
  http://www.furgovw.org/index.php?topic=330256.0
