# Fritzing sketch id2317_CD4094_control_using_smart_phone_0 (saved by Fritzing 0.7.0b)
breadboards: 1

parts:
  Q8 = LED - 3mm [color="Red (633nm)" package="3 mm [THT]"]
  Arduino2 = Arduino
  Q1 = LED - 3mm [color="Red (633nm)" package="3 mm [THT]"]
  R11 = Resistor [tolerance=±5% resistance=220 package=THT]
  R7 = Resistor [tolerance=±5% resistance=220 package=THT]
  Q2 = LED - 3mm [color="Red (633nm)" package="3 mm [THT]"]
  R3 = Resistor [tolerance=±5% resistance=220 package=THT]
  4094 = HEF4094 [package="DIP16 [THT]"]
  Q3 = LED - 3mm [color="Red (633nm)" package="3 mm [THT]"]
  Q5 = LED - 3mm [color="Red (633nm)" package="3 mm [THT]"]
  R12 = Resistor [tolerance=±5% resistance=220 package=THT]
  Q6 = LED - 3mm [color="Red (633nm)" package="3 mm [THT]"]
  R8 = Resistor [tolerance=±5% resistance=220 package=THT]
  R4 = Resistor [tolerance=±5% resistance=220 package=THT]
  Part1 = Bluetooth Mate Silver
  Q7 = LED - 3mm [color="Red (633nm)" package="3 mm [THT]"]
  QS' = LED - 3mm [color="Yellow (595nm)" package="3 mm [THT]"]
  R9 = Resistor [tolerance=±5% resistance=220 package=THT]
  R5 = Resistor [tolerance=±5% resistance=220 package=THT]
  QS = LED - 3mm [color="Orange (620nm)" package="3 mm [THT]"]
  Q4 = LED - 3mm [color="Red (633nm)" package="3 mm [THT]"]
  R10 = Resistor [tolerance=±5% resistance=220 package=THT]
  R6 = Resistor [tolerance=±5% resistance=220 package=THT]

nets:
  GND: Q8.cathode, Arduino2.GND, Q1.cathode, Q2.cathode, 4094.Vss, Q3.cathode, Q5.cathode, Q6.cathode, Part1.GND, Q7.cathode, QS'.cathode, QS.cathode, Q4.cathode
  N1: Q8.anode, R10.Pin_1
  N2: Arduino2.D12, 4094.STROBE
  N3: Arduino2.D10, 4094.CLOCK
  N4: Arduino2.D9, 4094.OE
  N5: Arduino2.D8, 4094.DATA
  N6: Arduino2.D1TX, Part1.RX_5V
  N7: Arduino2.D0RX, Part1.TX_5V
  +5V: Arduino2.+5V, 4094.Vdd, Part1.VCC
  N8: Q1.anode, R3.Pin_1
  N9: R11.Pin_0, QS.anode
  N10: R11.Pin_1, 4094.Qs
  N11: R7.Pin_0, 4094.Q5
  N12: R7.Pin_1, Q5.anode
  N13: Q2.anode, R4.Pin_1
  N14: R3.Pin_0, 4094.Q1
  N15: 4094.Q2, R4.Pin_0
  N16: 4094.Q3, R5.Pin_0
  N17: 4094.Q4, R6.Pin_0
  N18: 4094.Q's, R12.Pin_1
  N19: 4094.Q8, R10.Pin_0
  N20: 4094.Q7, R9.Pin_0
  N21: 4094.Q6, R8.Pin_0
  N22: Q3.anode, R5.Pin_1
  N23: R12.Pin_0, QS'.anode
  N24: Q6.anode, R8.Pin_1
  N25: Q7.anode, R9.Pin_1
  N26: Q4.anode, R6.Pin_1
