# Fritzing sketch id231_Actionneur_externe_0 (saved by Fritzing 0.9.3b)
breadboards: 1

parts:
  Composant1 = Arduino Leonardo (Rev3b)
  LED1 = LED - 5mm [color="Green (570nm)" package="5 mm [THT]"]
  LED2 = LED - 5mm [color="Red (633nm)" package="5 mm [THT]"]
  Power_plug1 = Power plug
  R1 = Resistor [tolerance=±5% resistance=220 package=THT]
  R2 = Resistor [tolerance=±5% resistance=220 package=THT]

nets:
  N1: Composant1.D2/SDA, R2.Pin_1
  N2: Composant1.D3_PWM/SCL, R1.Pin_0
  N3: LED1.cathode, R2.Pin_0
  N4: LED1.anode, LED2.anode, Power_plug1.GND
  N5: LED2.cathode, R1.Pin_1
