# Fritzing sketch id2321_schema_led_cube_0 (saved by Fritzing 0.8.3b)
breadboards: 1

parts:
  Arduino_1_Rev3 = Arduino Uno (Rev3)
  LED1 = LED - 5mm [color="Red (633nm)" package="5 mm [THT]"]
  LED2 = LED - 5mm [color="Red (633nm)" package="5 mm [THT]"]
  LED3 = LED - 5mm [color="Red (633nm)" package="5 mm [THT]"]
  LED4 = LED - 5mm [color="Red (633nm)" package="5 mm [THT]"]
  LED5 = LED - 5mm [color="Red (633nm)" package="5 mm [THT]"]
  LED6 = LED - 5mm [color="Red (633nm)" package="5 mm [THT]"]
  LED7 = LED - 5mm [color="Red (633nm)" package="5 mm [THT]"]
  LED8 = LED - 5mm [color="Red (633nm)" package="5 mm [THT]"]
  LED9 = LED - 5mm [color="Red (633nm)" package="5 mm [THT]"]
  LED10 = LED - 5mm [color="Red (633nm)" package="5 mm [THT]"]
  LED11 = LED - 5mm [color="Red (633nm)" package="5 mm [THT]"]
  LED12 = LED - 5mm [color="Red (633nm)" package="5 mm [THT]"]
  LED13 = LED - 5mm [color="Red (633nm)" package="5 mm [THT]"]
  LED14 = LED - 5mm [color="Red (633nm)" package="5 mm [THT]"]
  LED15 = LED - 5mm [color="Red (633nm)" package="5 mm [THT]"]
  LED16 = LED - 5mm [color="Red (633nm)" package="5 mm [THT]"]
  LED17 = LED - 5mm [color="Red (633nm)" package="5 mm [THT]"]
  LED18 = LED - 5mm [color="Red (633nm)" package="5 mm [THT]"]
  LED19 = LED - 5mm [color="Red (633nm)" package="5 mm [THT]"]
  LED20 = LED - 5mm [color="Red (633nm)" package="5 mm [THT]"]
  LED21 = LED - 5mm [color="Red (633nm)" package="5 mm [THT]"]
  LED22 = LED - 5mm [color="Red (633nm)" package="5 mm [THT]"]
  LED23 = LED - 5mm [color="Red (633nm)" package="5 mm [THT]"]
  LED24 = LED - 5mm [color="Red (633nm)" package="5 mm [THT]"]
  LED25 = LED - 5mm [color="Red (633nm)" package="5 mm [THT]"]
  LED26 = LED - 5mm [color="Red (633nm)" package="5 mm [THT]"]
  LED27 = LED - 5mm [color="Red (633nm)" package="5 mm [THT]"]
  Q1 = NPN-Transistor [package="TO92 [THT]"]
  Q2 = NPN-Transistor [package="TO92 [THT]"]
  Q3 = NPN-Transistor [package="TO92 [THT]"]
  R1 = Resistor [tolerance=±5% resistance=22k package=THT]
  R2 = Resistor [tolerance=±5% resistance=22k package=THT]
  R3 = Resistor [tolerance=±5% resistance=22k package=THT]

nets:
  N1: Arduino_1_Rev3.A0, Q1.B
  N2: Arduino_1_Rev3.A1, Q2.B
  N3: Arduino_1_Rev3.A2, Q3.B
  N4: Arduino_1_Rev3.GND, Q1.E, Q2.E, Q3.E
  N5: Arduino_1_Rev3.D8, LED1.anode, LED10.anode, LED19.cathode, LED19.anode, LED21.cathode, LED22.cathode, LED23.cathode, LED25.cathode, LED26.cathode
  N6: Arduino_1_Rev3.D9_PWM, LED2.anode, LED11.anode, LED20.anode
  N7: Arduino_1_Rev3.D10_PWM/SS, LED3.anode, LED12.anode, LED21.anode
  N8: Arduino_1_Rev3.D2, LED7.anode, LED15.anode, LED24.anode
  N9: Arduino_1_Rev3.D3_PWM, LED8.anode, LED16.anode, LED25.anode
  N10: Arduino_1_Rev3.D4, LED9.anode, LED17.anode, LED26.anode
  N11: Arduino_1_Rev3.D5_PWM, LED4.anode, LED14.anode, LED23.anode
  N12: Arduino_1_Rev3.D6_PWM, LED5.anode, LED18.anode, LED27.anode
  N13: Arduino_1_Rev3.D7, LED6.anode, LED13.anode, LED22.anode
  N14: LED1.cathode, LED3.cathode, LED4.cathode, LED6.cathode, LED8.cathode
  N15: LED2.cathode, LED5.cathode
  N16: LED9.cathode, R1.Pin_1
  N17: LED10.cathode, LED12.cathode, LED13.cathode, LED14.cathode, LED16.cathode, LED17.cathode
  N18: LED11.cathode, LED18.cathode
  N19: LED15.cathode, R2.Pin_1
  N20: LED20.cathode, LED27.cathode
  N21: LED24.cathode, R3.Pin_1
  N22: Q1.C, R1.Pin_0
  N23: Q2.C, R2.Pin_0
  N24: Q3.C, R3.Pin_0
