# Fritzing sketch id2322_cubeLed_0 (saved by Fritzing 0.9.3b)
breadboards: 1

parts:
  Part1 = Arduino Micro (Rev3)  # not connected
  VCC1 = 4 x AAA Battery Mount
  Q1 = Basic FET P-Channel [package="DPak [SMD]"]
  D1 = P1000K [part_number=P1000K]  # not connected
  R1 = Resistor [tolerance=±5% resistance=220 package="0603 [SMD]"]

nets:
  N1: VCC1.-, R1.Pin_1
  N2: VCC1.+, Q1.source
