# Fritzing sketch id2323_proyecto_led__modulo_2_0 (saved by Fritzing 0.7.5b)
breadboards: 1

parts:
  Arduino1 = Arduino
  R1 = Resistor [tolerance=±5% resistance=220 package=THT]
  R2 = Resistor [tolerance=±5% resistance=220 package=THT]
  R3 = Resistor [tolerance=±5% resistance=220 package=THT]
  R4 = Resistor [tolerance=±5% resistance=220 package=THT]
  LED1 = LED - 5mm [color="Red (633nm)" package="5 mm [THT]"]
  LED2 = LED - 5mm [color="Red (633nm)" package="5 mm [THT]"]
  LED3 = LED - 5mm [color="Red (633nm)" package="5 mm [THT]"]
  LED4 = LED - 5mm [color="Red (633nm)" package="5 mm [THT]"]
  LED5 = LED - 5mm [color="Yellow (595nm)" package="5 mm [THT]"]
  LED6 = LED - 5mm [color="Yellow (595nm)" package="5 mm [THT]"]
  LED7 = LED - 5mm [color="Yellow (595nm)" package="5 mm [THT]"]
  LED8 = LED - 5mm [color="Yellow (595nm)" package="5 mm [THT]"]
  LED9 = LED - 5mm [color="Green (570nm)" package="5 mm [THT]"]
  LED10 = LED - 5mm [color="Green (570nm)" package="5 mm [THT]"]
  LED11 = LED - 5mm [color="Green (570nm)" package="5 mm [THT]"]
  LED12 = LED - 5mm [color="Green (570nm)" package="5 mm [THT]"]

nets:
  N1: Arduino1.D12, LED10.anode
  N2: Arduino1.D11, LED8.anode
  N3: Arduino1.D10, LED4.anode
  N4: Arduino1.D9, LED12.anode
  N5: Arduino1.D8, LED6.anode
  N6: Arduino1.D7, LED1.anode
  N7: Arduino1.D6, LED11.anode
  N8: Arduino1.D5, LED7.anode
  N9: Arduino1.D4, LED3.anode
  N10: Arduino1.D3, LED9.anode
  N11: Arduino1.D2, LED5.anode
  N12: Arduino1.D1TX, LED2.anode
  N13: R1.Pin_1, R2.Pin_1
  N14: R2.Pin_0, LED8.cathode
  N15: R3.Pin_0, R4.Pin_1
  N16: R3.Pin_1, LED9.cathode
  N17: R4.Pin_0, LED7.cathode
  N18: LED3.cathode, LED11.cathode
