# Fritzing sketch id2324_UNO_PWM_INTRODUCTION_0 (saved by Fritzing 0.9.2b)
breadboards: 1

parts:
  Part1 = Arduino Uno (Rev3)
  R1 = Resistor [tolerance=±5% resistance=220 package=THT]
  LED1 = LED - 5mm [color="Red (633nm)" package="5 mm [THT]"]
  S1 = Pushbutton [package="[THT]"]
  S2 = Pushbutton [package="[THT]"]
  R2 = Resistor [tolerance=±5% resistance=220 package=THT]
  R3 = Resistor [tolerance=±5% resistance=220 package=THT]

nets:
  N1: Part1.GND, R1.Pin_1, S1.Pin_1, S1.Pin_2, S2.Pin_1, S2.Pin_2
  N2: Part1.D0/RX, S1.Pin_3, S1.Pin_4, R3.Pin_1
  N3: Part1.D1/TX, S2.Pin_3, S2.Pin_4, R2.Pin_0
  N4: Part1.D3_PWM, LED1.anode
  N5: Part1.5V, R2.Pin_1, R3.Pin_0
  N6: R1.Pin_0, LED1.cathode
