# Fritzing sketch id2325_proyecto_bot_alarma_0 (saved by Fritzing 0.9.3b)
breadboards: 1

parts:
  Componente1 = Arduino Uno (Rev3)
  J1 = Piezo Speaker
  LED1 = LED - 5mm [color="Red (633nm)" package="5 mm [THT]"]
  LED2 = LED - 5mm [color="Red (633nm)" package="5 mm [THT]"]
  R1 = Resistor [tolerance=±5% resistance=220 package=THT]
  R2 = Resistor [tolerance=±5% resistance=220 package=THT]
  Parte3 = HC-SR04 ultrasonic distance sensor

nets:
  N1: Componente1.D10_PWM/SS, Parte3.connector2
  N2: Componente1.D11_PWM/MOSI, Parte3.connector1
  N3: Componente1.GND, J1.pin1, R1.Pin_1, R2.Pin_1, Parte3.connector3
  N4: Componente1.D5_PWM, J1.pin2
  N5: Componente1.5V, Parte3.connector0
  N6: LED1.cathode, R1.Pin_0
  N7: LED2.cathode, R2.Pin_0
