# Fritzing sketch id2326_PCB_LED_Arduino_0 (saved by Fritzing 0.8.3b)
circuit board: 6.88561cm x 5.36311cm
stripboards: 1

parts:
  Phase_Focus_LED_Shield = Arduino Ethernet Shield
  Q1(R) = NPN-Transistor [package="TO92 [THT]"]
  R1(R) = Resistor [tolerance=±5% resistance=220 package=THT]
  R2(R) = Resistor [tolerance=±5% resistance=1 package=THT]
  Q2(R) = Basic FET P-Channel [package="TO220 [THT]"]
  Power_plug1 = Power plug
  R1(G) = Resistor [tolerance=±5% resistance=220 package=THT]
  R1(B) = Resistor [tolerance=±5% resistance=220 package=THT]
  Q1(G) = NPN-Transistor [package="TO92 [THT]"]
  Q2(G) = Basic FET P-Channel [package="TO220 [THT]"]
  R2(G) = Resistor [tolerance=±5% resistance=1 package=THT]
  Q1(B) = NPN-Transistor [package="TO92 [THT]"]
  Q2(B) = Basic FET P-Channel [package="TO220 [THT]"]
  R2(B) = Resistor [tolerance=±5% resistance=1 package=THT]
  R(150) = Resistor [tolerance=±5% resistance=1 package=THT]
  IC1 = Voltage Regulator [package=78xxl]
  R(150)1 = Resistor [tolerance=±5% resistance=1 package=THT]

nets:
  N1: Phase_Focus_LED_Shield.SS, R1(B).Pin_0
  N2: Phase_Focus_LED_Shield.D6, R1(G).Pin_0
  N3: Phase_Focus_LED_Shield.D5, R1(R).Pin_1
  N4: Phase_Focus_LED_Shield.+5V, R(150).Pin_1
  GND: Phase_Focus_LED_Shield.GND, IC1.GND
  N5: Q1(R).E, R2(R).Pin_0, Power_plug1.GND, Q1(G).E, R2(G).Pin_0, Q1(B).E, R2(B).Pin_0
  N6: Q1(R).B, R2(R).Pin_1, Q2(R).source
  N7: Q1(R).C, R1(R).Pin_0, Q2(R).gate
  N8: Power_plug1.VCC, IC1.IN
  N9: R1(G).Pin_1, Q1(G).C, Q2(G).gate
  N10: R1(B).Pin_1, Q1(B).C, Q2(B).gate
  N11: Q1(G).B, Q2(G).source, R2(G).Pin_1
  N12: Q1(B).B, Q2(B).source, R2(B).Pin_1
  N13: IC1.OUT, R(150)1.Pin_0

notes:
  Blue
  Red
  Green
  +
  USB pwr
  Shield pwr
