# Fritzing sketch id2327_2012_11_19_LED_Stromquelle_SMD_fill_0 (saved by Fritzing 0.7.10b)
breadboards: 1

parts:
  Q2 = NPN-Transistor [package="SOT-23 [SMD]"]
  Q1 = NPN-Transistor [package="SOT-23 [SMD]"]
  R1 = Resistor [tolerance=±5% resistance=4.7k package="1206 [SMD]"]
  R2 = Resistor [tolerance=±5% resistance=22 package="1206 [SMD]"]
  V+ = Pad [width=3 height=3 connect=center]
  A = Pad [width=3 height=3 connect=center]
  K = Pad [width=3 height=3 connect=center]
  GND = Pad [width=3 height=3 connect=center]

nets:
  N1: Q2.2, Q1.0, R2.Pin_0
  N2: Q2.0, Q1.1, R1.Pin_1
  N3: Q2.1, K.pad
  N4: Q1.2, R2.Pin_1, GND.pad
  N5: R1.Pin_0, V+.pad, A.pad

notes:
  LED Stromquelle in SMD für Modellbau, v0
  4 ... 24 V
  LED Kathode
  GND
  LED Anode
  LED
  Treiber
  JFS
