# Fritzing sketch id2328_LED_Dice_0 (saved by Fritzing 0.9.0b)
breadboards: 1

parts:
  R1 = Resistor [tolerance=±5% resistance=220 package=THT]
  S1 = Pushbutton [package="[THT]"]
  R2 = Resistor [tolerance=±5% resistance=100k package=THT]
  Part1 = Arduino Uno (Rev3)
  LED1 = LED - 5mm [color="Red (633nm)" package="5 mm [THT]"]
  LED2 = LED - 5mm [color="Red (633nm)" package="5 mm [THT]"]
  LED3 = LED - 5mm [color="Red (633nm)" package="5 mm [THT]"]
  R3 = Resistor [tolerance=±5% resistance=220 package=THT]
  R4 = Resistor [tolerance=±5% resistance=220 package=THT]
  LED4 = LED - 5mm [color="Red (633nm)" package="5 mm [THT]"]
  LED5 = LED - 5mm [color="Red (633nm)" package="5 mm [THT]"]
  LED6 = LED - 5mm [color="Red (633nm)" package="5 mm [THT]"]
  LED7 = LED - 5mm [color="Red (633nm)" package="5 mm [THT]"]
  R5 = Resistor [tolerance=±5% resistance=220 package=THT]
  R6 = Resistor [tolerance=±5% resistance=220 package=THT]
  R7 = Resistor [tolerance=±5% resistance=220 package=THT]
  R8 = Resistor [tolerance=±5% resistance=220 package=THT]

nets:
  N1: R1.Pin_0, R2.Pin_0, R3.Pin_0, R4.Pin_0, R5.Pin_0, R6.Pin_0, R7.Pin_0, R8.Pin_0
  N2: R1.Pin_1, LED1.cathode
  N3: S1.Pin_1, S1.Pin_2
  N4: S1.Pin_3, S1.Pin_4, R2.Pin_1, Part1.D9_PWM
  N5: Part1.D8, LED7.anode
  N6: Part1.D2, LED3.anode
  N7: Part1.D3_PWM, LED2.anode
  N8: Part1.D4, LED1.anode
  N9: Part1.D5_PWM, LED6.anode
  N10: Part1.D6_PWM, LED5.anode
  N11: Part1.D7, LED4.anode
  N12: LED2.cathode, R3.Pin_1
  N13: LED3.cathode, R4.Pin_1
  N14: LED4.cathode, R5.Pin_1
  N15: LED5.cathode, R6.Pin_1
  N16: LED6.cathode, R7.Pin_1
  N17: LED7.cathode, R8.Pin_1
