# Fritzing sketch id232_Activador_VE_con_voltaje_0 (saved by Fritzing 0.9.3b)
breadboards: 1

parts:
  R1 = Rotary Potentiometer (Small) [maximum_resistance=100kΩ package=THT]  # not connected
  S1 = Pushbutton [package="[THT]"]
  Componente1 = Arduino Uno (Rev3)
  Componente2 = RFID-RC522v3
  Componente3 = LCD1602-I2C_
  LED2 = RGB LED (com. cathode, rgb) [package="5 mm [THT]"]
  R2 = Resistor [tolerance=±5% resistance=220 package="0402 [SMD]"]
  R3 = Resistor [tolerance=±5% resistance=220 package="0402 [SMD]"]
  R4 = Resistor [tolerance=±5% resistance=220 package="0402 [SMD]"]
  OMRON1 = OMRON PCB Power Relay – G5LE [part_number="G5LE-1\n" package=THT]
  R5 = Resistor [tolerance=±5% resistance=220 package=THT]
  LED3 = LED - 5mm [color="Red (633nm)" package="5 mm [THT]"]

nets:
  N1: S1.Pin_1, S1.Pin_2, Componente1.D3_PWM
  N2: S1.Pin_3, S1.Pin_4, Componente1.GND, Componente2.connector13, Componente3.connector0, LED2.common_cathode, OMRON1.COIL1, LED3.cathode
  N3: Componente1.D9_PWM, Componente2.connector14
  N4: Componente1.D10_PWM/SS, Componente2.connector8
  N5: Componente1.D11_PWM/MOSI, Componente2.connector10
  N6: Componente1.D12/MISO, Componente2.connector11
  N7: Componente1.D13/SCK, Componente2.connector9
  N8: Componente1.A4/SDA, Componente3.connector2
  N9: Componente1.A5/SCL, Componente3.connector3
  N10: Componente1.D4, OMRON1.C
  N11: Componente1.D5_PWM, R2.Pin_1
  N12: Componente1.D6_PWM, R3.Pin_1
  N13: Componente1.D7, R4.Pin_0
  N14: Componente1.3V3, Componente2.connector15
  N15: Componente1.5V, Componente3.connector1, OMRON1.COIL2
  N16: LED2.red_anode, R4.Pin_1
  N17: LED2.green_anode, R3.Pin_0
  N18: LED2.blue_anode, R2.Pin_0
  N19: OMRON1.B, R5.Pin_0
  N20: R5.Pin_1, LED3.anode
