# Fritzing sketch id2330_LED_Fade_fritzing_0 (saved by Fritzing 0.9.3b)
breadboards: 1

parts:
  부품1 = Arduino Uno (Rev3)
  LED1 = smd LED [color="Red (633nm)" package="1206 [SMD]"]
  R1 = Resistor [tolerance=±5% resistance=220 package="2512 [SMD]"]

nets:
  N1: 부품1.D9_PWM, LED1.anode
  N2: 부품1.GND, R1.Pin_0
  N3: LED1.cathode, R1.Pin_1
