# Fritzing sketch id2331_fader_v3_0 (saved by Fritzing 0.7.6b)
breadboards: 1

parts:
  Part1 = Arduino Pro Mini 3.3V
  VCC1 = Battery block 9V
  Q1 = Basic FET N-Channel [part_number=nte2382 package="TO220 [THT]"]
  Q2 = Basic FET N-Channel [part_number=nte2382 package="TO220 [THT]"]
  U1 = Voltage Regulator - 5V [part_number=nte1932 package="TO220 [THT]"]
  D1 = Rectifier Diode [part_number=4002-9745 package="300 mil [THT]"]
  D2 = Rectifier Diode [part_number=4002-9745 package="300 mil [THT]"]
  S1_-_PWR = Pushbutton [package="[THT]"]
  R1 = Resistor [tolerance=±5% resistance=10k package=THT]
  S2 = Pushbutton [package="[THT]"]
  R2 = Resistor [tolerance=±5% resistance=10k package=THT]
  R3 = Resistor [tolerance=±5% resistance=10k package=THT]
  S3 = Pushbutton [package="[THT]"]
  LED1 = LED - 5mm [color="White (4500K)" package="5 mm [THT]"]
  R4 = Resistor [tolerance=±5% resistance=220 package=THT]
  LED2 = LED - 5mm [color="Red (633nm)" package="5 mm [THT]"]
  CHG- = Pad [width=2.96333333333333 height=2.96333333333333 connect=center]  # not connected
  CHG-_2 = Pad [width=2.96333333333333 height=2.96333333333333 connect=center]  # not connected
  LED- = Pad [width=4.02166666666667 height=3.73944444444444 connect=center]  # not connected
  Batt+ = Pad [width=2.96333333333333 height=2.96333333333333 connect=center]  # not connected
  DC_Power1 = DC Power [voltage=5]
  R5 = Resistor [tolerance=±5% resistance=10k package=THT]
  Batt- = Pad [width=2.96333333333333 height=2.96333333333333 connect=center]  # not connected
  LED+ = Pad [width=2.96333333333333 height=2.96333333333333 connect=center]  # not connected

nets (from the schematic view):
  N1: Part1.VCC, R1.Pin_1, S2.Pin_3, S2.Pin_4, S3.Pin_3, S3.Pin_4
  GND: Part1.GND, VCC1.-, Q1.source, Q2.source, U1.GND, D2.anode, S1_-_PWR.Pin_3, S1_-_PWR.Pin_4, R1.Pin_0, R2.Pin_1, R3.Pin_1, LED2.cathode, R5.Pin_1
  N2: Part1.RAW, U1.output_voltage
  N3: Part1.D8, R4.Pin_1
  N4: Part1.D6, Q1.gate, Q2.gate
  N5: Part1.D5, D1.anode, DC_Power1.V+, R5.Pin_0
  N6: Part1.D4, R2.Pin_0, S3.Pin_1, S3.Pin_2
  N7: Part1.D3, S2.Pin_1, S2.Pin_2, R3.Pin_0
  N8: Part1.D2, S1_-_PWR.Pin_1, S1_-_PWR.Pin_2
  N9: VCC1.+, U1.input_voltage, D1.cathode, LED1.anode
  N10: Q1.drain, Q2.drain, LED1.cathode
  N11: D2.cathode, DC_Power1.GND
  N12: R4.Pin_0, LED2.anode
