# Fritzing sketch id2332_Flash_0 (saved by Fritzing 0.9.3b)
breadboards: 1

parts:
  C1 = Electrolytic Capacitor [capacitance=1µF package="100 mil [THT, electrolytic]"]  # not connected
  C2 = Electrolytic Capacitor [capacitance=1mF package="100 mil [THT, electrolytic]"]
  LED1 = LED - 3mm [color="Red (633nm)" package="3 mm [THT]"]
  VCC1 = Battery block 9V
  R1 = Resistor [tolerance=±5% resistance=6.8 package=THT]
  R2 = Resistor [tolerance=±5% resistance=3.3 package=THT]
  S2 = Pushbutton [package=THT]

nets:
  N1: C2.-, R1.Pin_1
  N2: C2.+, S2.leg1
  N3: LED1.cathode, R2.Pin_1
  N4: LED1.anode, VCC1.-
  N5: VCC1.+, R1.Pin_0
  N6: R2.Pin_0, S2.leg0
