# Fritzing sketch id2333_LED_Intermediate3x3b_0 (saved by Fritzing 0.9.2b)
circuit board: 6.88566cm x 5.36311cm
breadboards: 1

parts:
  Part1 = Arduino Uno (Rev3)
  LED1 = LED - 5mm [color="Red (633nm)" package="5 mm [THT]"]
  LED2 = LED - 5mm [color="Red (633nm)" package="5 mm [THT]"]
  LED3 = LED - 5mm [color="Red (633nm)" package="5 mm [THT]"]
  LED4 = LED - 5mm [color="Red (633nm)" package="5 mm [THT]"]
  LED5 = LED - 5mm [color="Red (633nm)" package="5 mm [THT]"]
  LED6 = LED - 5mm [color="Red (633nm)" package="5 mm [THT]"]
  LED7 = LED - 5mm [color="Red (633nm)" package="5 mm [THT]"]
  LED8 = LED - 5mm [color="Red (633nm)" package="5 mm [THT]"]
  LED9 = LED - 5mm [color="Red (633nm)" package="5 mm [THT]"]
  R1 = Resistor [tolerance=±5% resistance=220 package=THT]
  R2 = Resistor [tolerance=±5% resistance=220 package=THT]
  R3 = Resistor [tolerance=±5% resistance=220 package=THT]

nets:
  N1: Part1.D2, LED3.anode, LED6.anode, LED9.anode
  N2: Part1.D3_PWM, LED2.anode, LED5.anode, LED8.anode
  N3: Part1.D4, LED1.anode, LED4.anode, LED7.anode
  N4: Part1.D5_PWM, R1.Pin_0
  N5: Part1.D6_PWM, R2.Pin_0
  N6: Part1.D7, R3.Pin_0
  N7: LED1.cathode, LED2.cathode, LED3.cathode, R3.Pin_1
  N8: LED4.cathode, LED5.cathode, LED6.cathode, R2.Pin_1
  N9: LED7.cathode, LED8.cathode, LED9.cathode, R1.Pin_1
