# Fritzing sketch id2334_schematic_0 (saved by Fritzing 0.9.0b)

parts:
  LED1 = LED - 3mm [color="Blue (430nm)" package="3 mm [THT]"]
  LED2 = LED - 3mm [color="Blue (430nm)" package="3 mm [THT]"]
  LED3 = LED - 3mm [color="Blue (430nm)" package="3 mm [THT]"]
  LED4 = LED - 3mm [color="Blue (430nm)" package="3 mm [THT]"]
  LED5 = LED - 3mm [color="Blue (430nm)" package="3 mm [THT]"]
  LED6 = LED - 3mm [color="Blue (430nm)" package="3 mm [THT]"]
  LED7 = LED - 3mm [color="Blue (430nm)" package="3 mm [THT]"]
  LED8 = LED - 3mm [color="Blue (430nm)" package="3 mm [THT]"]
  LED9 = LED - 3mm [color="Blue (430nm)" package="3 mm [THT]"]
  LED10 = LED - 3mm [color="Blue (430nm)" package="3 mm [THT]"]
  LED11 = LED - 3mm [color="Blue (430nm)" package="3 mm [THT]"]
  LED12 = LED - 3mm [color="Blue (430nm)" package="3 mm [THT]"]
  LED13 = LED - 3mm [color="Blue (430nm)" package="3 mm [THT]"]
  LED14 = LED - 3mm [color="Blue (430nm)" package="3 mm [THT]"]
  LED15 = LED - 3mm [color="Blue (430nm)" package="3 mm [THT]"]
  LED16 = LED - 3mm [color="Blue (430nm)" package="3 mm [THT]"]
  LED17 = LED - 3mm [color="Blue (430nm)" package="3 mm [THT]"]
  LED18 = LED - 3mm [color="Blue (430nm)" package="3 mm [THT]"]
  LED19 = LED - 3mm [color="Blue (430nm)" package="3 mm [THT]"]
  LED20 = LED - 3mm [color="Blue (430nm)" package="3 mm [THT]"]
  LED21 = LED - 3mm [color="Blue (430nm)" package="3 mm [THT]"]
  LED22 = LED - 3mm [color="Blue (430nm)" package="3 mm [THT]"]
  LED23 = LED - 3mm [color="Blue (430nm)" package="3 mm [THT]"]
  LED24 = LED - 3mm [color="Blue (430nm)" package="3 mm [THT]"]
  LED25 = LED - 3mm [color="Blue (430nm)" package="3 mm [THT]"]
  LED26 = LED - 3mm [color="Blue (430nm)" package="3 mm [THT]"]
  LED27 = LED - 3mm [color="Blue (430nm)" package="3 mm [THT]"]
  LED28 = LED - 3mm [color="Blue (430nm)" package="3 mm [THT]"]
  LED29 = LED - 3mm [color="Blue (430nm)" package="3 mm [THT]"]
  LED30 = LED - 3mm [color="Blue (430nm)" package="3 mm [THT]"]
  LED31 = LED - 3mm [color="Blue (430nm)" package="3 mm [THT]"]
  LED32 = LED - 3mm [color="Blue (430nm)" package="3 mm [THT]"]
  LED33 = LED - 3mm [color="Blue (430nm)" package="3 mm [THT]"]
  LED34 = LED - 3mm [color="Blue (430nm)" package="3 mm [THT]"]
  LED35 = LED - 3mm [color="Blue (430nm)" package="3 mm [THT]"]
  LED36 = LED - 3mm [color="Blue (430nm)" package="3 mm [THT]"]
  LED37 = LED - 3mm [color="Blue (430nm)" package="3 mm [THT]"]
  LED38 = LED - 3mm [color="Blue (430nm)" package="3 mm [THT]"]
  LED39 = LED - 3mm [color="Blue (430nm)" package="3 mm [THT]"]
  LED40 = LED - 3mm [color="Blue (430nm)" package="3 mm [THT]"]
  LED41 = LED - 3mm [color="Blue (430nm)" package="3 mm [THT]"]
  LED42 = LED - 3mm [color="Blue (430nm)" package="3 mm [THT]"]
  LED43 = LED - 3mm [color="Blue (430nm)" package="3 mm [THT]"]
  LED44 = LED - 3mm [color="Blue (430nm)" package="3 mm [THT]"]
  LED45 = LED - 3mm [color="Blue (430nm)" package="3 mm [THT]"]
  LED46 = LED - 3mm [color="Blue (430nm)" package="3 mm [THT]"]
  LED47 = LED - 3mm [color="Blue (430nm)" package="3 mm [THT]"]
  LED48 = LED - 3mm [color="Blue (430nm)" package="3 mm [THT]"]
  LED49 = LED - 3mm [color="Blue (430nm)" package="3 mm [THT]"]
  LED50 = LED - 3mm [color="Blue (430nm)" package="3 mm [THT]"]
  LED51 = LED - 3mm [color="Blue (430nm)" package="3 mm [THT]"]
  LED52 = LED - 3mm [color="Blue (430nm)" package="3 mm [THT]"]
  LED53 = LED - 3mm [color="Blue (430nm)" package="3 mm [THT]"]
  LED54 = LED - 3mm [color="Blue (430nm)" package="3 mm [THT]"]
  LED55 = LED - 3mm [color="Blue (430nm)" package="3 mm [THT]"]
  LED56 = LED - 3mm [color="Blue (430nm)" package="3 mm [THT]"]
  LED57 = LED - 3mm [color="Blue (430nm)" package="3 mm [THT]"]
  LED58 = LED - 3mm [color="Blue (430nm)" package="3 mm [THT]"]
  LED59 = LED - 3mm [color="Blue (430nm)" package="3 mm [THT]"]
  LED60 = LED - 3mm [color="Blue (430nm)" package="3 mm [THT]"]
  LED61 = LED - 3mm [color="Blue (430nm)" package="3 mm [THT]"]
  LED62 = LED - 3mm [color="Blue (430nm)" package="3 mm [THT]"]
  LED63 = LED - 3mm [color="Blue (430nm)" package="3 mm [THT]"]
  LED64 = LED - 3mm [color="Blue (430nm)" package="3 mm [THT]"]
  R1 = Resistor [tolerance=±5% resistance=330 package=THT]
  R2 = Resistor [tolerance=±5% resistance=330 package=THT]
  R3 = Resistor [tolerance=±5% resistance=330 package=THT]
  R4 = Resistor [tolerance=±5% resistance=330 package=THT]
  R5 = Resistor [tolerance=±5% resistance=330 package=THT]
  R6 = Resistor [tolerance=±5% resistance=330 package=THT]
  R7 = Resistor [tolerance=±5% resistance=330 package=THT]
  R8 = Resistor [tolerance=±5% resistance=330 package=THT]
  R9 = Resistor [tolerance=±5% resistance=330 package=THT]
  R10 = Resistor [tolerance=±5% resistance=330 package=THT]
  R11 = Resistor [tolerance=±5% resistance=330 package=THT]
  R12 = Resistor [tolerance=±5% resistance=330 package=THT]
  R13 = Resistor [tolerance=±5% resistance=330 package=THT]
  R14 = Resistor [tolerance=±5% resistance=330 package=THT]
  R15 = Resistor [tolerance=±5% resistance=330 package=THT]
  R16 = Resistor [tolerance=±5% resistance=330 package=THT]
  Part1 = Arduino Uno (Rev3)
  S1 = Toggle Switch [package=THT]
  U1 = BNC [package=bnc]
  VCC1 = Battery

nets:
  N1: LED1.cathode, LED2.cathode, LED3.cathode, LED4.cathode, LED5.cathode, LED6.cathode, LED7.cathode, LED8.cathode, LED9.cathode, LED10.cathode, LED11.cathode, LED12.cathode, LED13.cathode, LED14.cathode, LED15.cathode, LED16.cathode, Part1.A2
  N2: LED1.anode, LED19.anode, LED35.anode, LED51.anode, R5.Pin_0
  N3: LED2.anode, LED26.anode, LED42.anode, LED58.anode, R8.Pin_0
  N4: LED3.anode, LED27.anode, LED43.anode, LED59.anode, R6.Pin_0
  N5: LED4.anode, LED24.anode, LED40.anode, LED56.anode, R7.Pin_0
  N6: LED5.anode, LED29.anode, LED45.anode, LED61.anode, R1.Pin_0
  N7: LED6.anode, LED28.anode, LED44.anode, LED60.anode, R4.Pin_0
  N8: LED7.anode, LED17.anode, LED33.anode, LED49.anode, R3.Pin_0
  N9: LED8.anode, LED21.anode, LED37.anode, LED53.anode, R2.Pin_0
  N10: LED9.anode, LED25.anode, LED41.anode, LED57.anode, R9.Pin_0
  N11: LED10.anode, LED22.anode, LED38.anode, LED54.anode, R11.Pin_0
  N12: LED11.anode, LED18.anode, LED34.anode, LED50.anode, R10.Pin_0
  N13: LED12.anode, LED30.anode, LED46.anode, LED62.anode, R12.Pin_0
  N14: LED13.anode, LED20.anode, LED36.anode, LED52.anode, R13.Pin_0
  N15: LED14.anode, LED23.anode, LED39.anode, LED55.anode, R15.Pin_0
  N16: LED15.anode, LED32.anode, LED48.anode, LED64.anode, R14.Pin_0
  N17: LED16.anode, LED31.anode, LED47.anode, LED63.anode, R16.Pin_0
  N18: LED17.cathode, LED18.cathode, LED19.cathode, LED20.cathode, LED21.cathode, LED22.cathode, LED23.cathode, LED24.cathode, LED25.cathode, LED26.cathode, LED27.cathode, LED28.cathode, LED29.cathode, LED30.cathode, LED31.cathode, LED32.cathode, Part1.A3
  N19: LED33.cathode, LED34.cathode, LED35.cathode, LED36.cathode, LED37.cathode, LED38.cathode, LED39.cathode, LED40.cathode, LED41.cathode, LED42.cathode, LED43.cathode, LED44.cathode, LED45.cathode, LED46.cathode, LED47.cathode, LED48.cathode, Part1.A4/SDA
  N20: LED49.cathode, LED50.cathode, LED51.cathode, LED52.cathode, LED53.cathode, LED54.cathode, LED55.cathode, LED56.cathode, LED57.cathode, LED58.cathode, LED59.cathode, LED60.cathode, LED61.cathode, LED62.cathode, LED63.cathode, LED64.cathode, Part1.A5/SCL
  N21: R1.Pin_1, Part1.D0/RX
  N22: R2.Pin_1, Part1.D1/TX
  N23: R3.Pin_1, Part1.D2
  N24: R4.Pin_1, Part1.D3_PWM
  N25: R5.Pin_1, Part1.D4
  N26: R6.Pin_1, Part1.D6_PWM
  N27: R7.Pin_1, Part1.D7
  N28: R8.Pin_1, Part1.D5_PWM
  N29: R9.Pin_1, Part1.D8
  N30: R10.Pin_1, Part1.D10_PWM/SS
  N31: R11.Pin_1, Part1.D11_PWM/MOSI
  N32: R12.Pin_1, Part1.D9_PWM
  N33: R13.Pin_1, Part1.D12/MISO
  N34: R14.Pin_1, Part1.A0
  N35: R15.Pin_1, Part1.A1
  N36: R16.Pin_1, Part1.D13/SCK
  N37: S1.L1, U1.GND
  N38: S1.COM, VCC1.-
  N39: U1.OUT, VCC1.+
