# Fritzing sketch id2336_LED_Light_Chaser_with_Raspberry_Pi_0 (saved by Fritzing 0.9.3b)
breadboards: 1

parts:
  Raspberry_Pi_1 = Raspberry Pi 3 [part_number=RPI-3-V1.2]
  R1 = Resistor [tolerance=±5% resistance=220 package="0805 [SMD]"]
  R2 = Resistor [tolerance=±5% resistance=220 package="0805 [SMD]"]
  R3 = Resistor [tolerance=±5% resistance=220 package="0805 [SMD]"]
  R4 = Resistor [tolerance=±5% resistance=220 package="0805 [SMD]"]
  R5 = Resistor [tolerance=±5% resistance=220 package="0805 [SMD]"]
  R6 = Resistor [tolerance=±5% resistance=470 package=THT]
  R7 = Resistor [tolerance=±5% resistance=470 package=THT]
  LED8 = LED - 5mm [color="Red (633nm)" package="5 mm [THT]"]
  LED4 = LED - 5mm [color="Red (633nm)" package="5 mm [THT]"]
  LED6 = LED - 5mm [color="Red (633nm)" package="5 mm [THT]"]
  LED7 = LED - 5mm [color="Red (633nm)" package="5 mm [THT]"]
  LED3 = LED - 5mm [color="Red (633nm)" package="5 mm [THT]"]
  LED2 = LED - 5mm [color="Red (633nm)" package="5 mm [THT]"]
  LED5 = LED - 5mm [color="Red (633nm)" package="5 mm [THT]"]

nets:
  N1: Raspberry_Pi_1.GPIO8, R6.Pin_1
  N2: Raspberry_Pi_1.GPIO25, R7.Pin_1
  N3: Raspberry_Pi_1.GPIO24, R5.Pin_1
  N4: Raspberry_Pi_1.GPIO23, R4.Pin_1
  N5: Raspberry_Pi_1.GPIO18, R3.Pin_1
  N6: Raspberry_Pi_1.GPIO15, R2.Pin_1
  N7: Raspberry_Pi_1.GPIO14, R1.Pin_1
  N8: Raspberry_Pi_1.GND, LED8.cathode, LED4.cathode, LED6.cathode, LED7.cathode, LED3.cathode, LED2.cathode, LED5.cathode
  N9: R1.Pin_0, LED4.anode
  N10: R2.Pin_0, LED2.anode
  N11: R3.Pin_0, LED3.anode
  N12: R4.Pin_0, LED5.anode
  N13: R5.Pin_0, LED6.anode
  N14: R6.Pin_0, LED8.anode
  N15: R7.Pin_0, LED7.anode
