# Fritzing sketch id2337_LED_Lightshow_0 (saved by Fritzing 0.9.2b)
breadboards: 1

parts:
  Raspberry_Pi1 = Raspberry Pi 2
  R1 = Resistor [tolerance=±5% resistance=220 package="1206 [SMD]"]
  R2 = Resistor [tolerance=±5% resistance=220 package="1206 [SMD]"]
  R3 = Resistor [tolerance=±5% resistance=220 package="1206 [SMD]"]
  R4 = Resistor [tolerance=±5% resistance=220 package="1206 [SMD]"]
  R5 = Resistor [tolerance=±5% resistance=220 package="1206 [SMD]"]
  R6 = Resistor [tolerance=±5% resistance=220 package="1206 [SMD]"]
  LED1 = LED - 3mm [color="Red (633nm)" package="3 mm [THT]"]
  LED2 = LED - 3mm [color="Red (633nm)" package="3 mm [THT]"]
  LED3 = LED - 3mm [color="Red (633nm)" package="3 mm [THT]"]
  LED4 = LED - 3mm [color="Red (633nm)" package="3 mm [THT]"]
  LED5 = LED - 3mm [color="Red (633nm)" package="3 mm [THT]"]
  LED6 = LED - 3mm [color="Red (633nm)" package="3 mm [THT]"]

nets:
  N1: Raspberry_Pi1.GPIO22, R6.Pin_1
  N2: Raspberry_Pi1.GPIO19, R5.Pin_1
  N3: Raspberry_Pi1.GPIO25, R4.Pin_1
  N4: Raspberry_Pi1.GPIO24, R3.Pin_1
  N5: Raspberry_Pi1.GPIO23, R2.Pin_1
  N6: Raspberry_Pi1.GPIO18, R1.Pin_1
  N7: Raspberry_Pi1.GND, LED1.cathode, LED2.cathode, LED3.cathode, LED4.cathode, LED5.cathode, LED6.cathode
  N8: R1.Pin_0, LED1.anode
  N9: R2.Pin_0, LED2.anode
  N10: R3.Pin_0, LED5.anode
  N11: R4.Pin_0, LED4.anode
  N12: R5.Pin_0, LED6.anode
  N13: R6.Pin_0, LED3.anode
