# Fritzing sketch id233_piano_0 (saved by Fritzing 0.9.2b)
breadboards: 1

parts:
  S1 = Pushbutton [package="[THT]"]
  S2 = Pushbutton [package="[THT]"]
  S3 = Pushbutton [package="[THT]"]
  S4 = Pushbutton [package="[THT]"]
  S5 = Pushbutton [package="[THT]"]
  S6 = Pushbutton [package="[THT]"]
  S7 = Pushbutton [package="[THT]"]
  Part1 = Arduino Uno (Rev3)
  R1 = Resistor [tolerance=±5% resistance=220 package=THT]
  R2 = Resistor [tolerance=±5% resistance=220 package=THT]
  R3 = Resistor [tolerance=±5% resistance=220 package=THT]
  R4 = Resistor [tolerance=±5% resistance=220 package=THT]
  R5 = Resistor [tolerance=±5% resistance=220 package=THT]
  R6 = Resistor [tolerance=±5% resistance=220 package=THT]
  R7 = Resistor [tolerance=±5% resistance=220 package=THT]
  J1 = Piezo Speaker
  R8 = Resistor [tolerance=±5% resistance=220 package=THT]

nets:
  N1: S1.Pin_1, S1.Pin_2, Part1.D8, R7.Pin_1
  N2: S1.Pin_3, S1.Pin_4, S3.Pin_3, S3.Pin_4, S4.Pin_3, S4.Pin_4, S5.Pin_3, S5.Pin_4, S6.Pin_3, S6.Pin_4, S7.Pin_3, S7.Pin_4, Part1.GND, J1.pin1
  N3: S2.Pin_1, S2.Pin_2, Part1.D2, R1.Pin_0
  N4: S2.Pin_3, S2.Pin_4
  N5: S3.Pin_1, S3.Pin_2, Part1.D3_PWM, R2.Pin_1
  N6: S4.Pin_1, S4.Pin_2, Part1.D4, R3.Pin_1
  N7: S5.Pin_1, S5.Pin_2, Part1.D5_PWM, R4.Pin_1
  N8: S6.Pin_1, S6.Pin_2, Part1.D6_PWM, R5.Pin_1
  N9: S7.Pin_1, S7.Pin_2, Part1.D7, R6.Pin_1
  N10: Part1.D11_PWM/MOSI, R8.Pin_1
  N11: Part1.5V, R1.Pin_1, R2.Pin_0, R3.Pin_0, R4.Pin_0, R5.Pin_0, R6.Pin_0, R7.Pin_0
  N12: J1.pin2, R8.Pin_0
