# Fritzing sketch id2340_matrix_0 (saved by Fritzing 0.7.4b)
breadboards: 1

parts:
  Arduino1 = Arduino
  Dot_Matrix1 = LED Dot Matrix 18mm (0.7 INCH)
  R1 = Rotary Potentiometer (Small) [maximum_resistance=100kΩ]

nets:
  N1: Arduino1.D12, Dot_Matrix1.Row_1
  N2: Arduino1.D11, Dot_Matrix1.Row_2
  N3: Arduino1.D10, Dot_Matrix1.Column_3
  N4: Arduino1.D9, Dot_Matrix1.Row_4
  N5: Arduino1.D8, Dot_Matrix1.Column_5
  N6: Arduino1.D7, Dot_Matrix1.Column_4
  N7: Arduino1.D6, Dot_Matrix1.Row_7
  N8: Arduino1.D5, Dot_Matrix1.Row_6
  N9: Arduino1.D4, Dot_Matrix1.Row_5
  N10: Arduino1.D3, Dot_Matrix1.Column_2
  N11: Arduino1.D2, Dot_Matrix1.Row_3
  N12: Arduino1.D1TX, Dot_Matrix1.Column_1
  N13: Arduino1.+5V, R1.leg1
  N14: Arduino1.GND, R1.leg2
  N15: Arduino1.A0, R1.wiper
