# Fritzing sketch id2341_disp8x8_0 (saved by Fritzing 0.9.3b)

parts:
  Disp1 = LBT2088AH [part_number=LBT2088AH]
  U1 = MAX7219 [package=dil24]
  Součástka1 = Arduino Uno (Rev3)
  R1 = Resistor [tolerance=±5% resistance=20k package=THT]
  GY1 = MPU-6050 GY-521 [form="♀ (female)"]

nets:
  N1: Disp1.pin1, U1.SEGD
  N2: Disp1.pin2, U1.SEGF
  N3: Disp1.pin_3, U1.DIG1
  N4: Disp1.pin_4, U1.DIG2
  N5: Disp1.pin_5, U1.SEGG
  N6: Disp1.pin_6, U1.DIG4
  N7: Disp1.pin_7, U1.SEGE
  N8: Disp1.pin_8, U1.SEGB
  N9: Disp1.pin_9, U1.SEGDP
  N10: Disp1.pin_10, U1.DIG3
  N11: Disp1.pin_11, U1.DIG5
  N12: Disp1.pin_12, U1.SEGC
  N13: Disp1.pin_13, U1.DIG0
  N14: Disp1.pin_14, U1.SEGA
  N15: Disp1.pin_15, U1.DIG6
  N16: Disp1.pin_16, U1.DIG7
  N17: U1.DIN, Součástka1.D12/MISO
  GND: U1.GND, U1.GND2, Součástka1.GND, GY1.connector1
  N18: U1.LOAD, Součástka1.D10_PWM/SS
  N19: U1.CLK, Součástka1.D11_PWM/MOSI
  N20: U1.ISET, R1.Pin_1
  VCC: U1.VCC, Součástka1.5V, R1.Pin_0
  N21: Součástka1.A4/SDA, GY1.connector3
  N22: Součástka1.A5/SCL, GY1.connector2
  N23: Součástka1.D2, GY1.connector7
  N24: Součástka1.3V3, GY1.connector0
