# Fritzing sketch id2342_Act_9_0 (saved by Fritzing 0.9.3b)
breadboards: 2

parts:
  Part1 = Arduino Uno (Rev3)
  Disp1 = LBT2088AH [part_number=LBT2088AH]

nets:
  N1: Part1.A0, Disp1.pin_6
  N2: Part1.A1, Disp1.pin_11
  N3: Part1.A2, Disp1.pin_15
  N4: Part1.A3, Disp1.pin_16
  N5: Part1.D8, Disp1.pin_14
  N6: Part1.D9_PWM, Disp1.pin_9
  N7: Part1.D10_PWM/SS, Disp1.pin_13
  N8: Part1.D11_PWM/MOSI, Disp1.pin_3
  N9: Part1.D12/MISO, Disp1.pin_4
  N10: Part1.D13/SCK, Disp1.pin_10
  N11: Part1.D2, Disp1.pin_5
  N12: Part1.D3_PWM, Disp1.pin2
  N13: Part1.D4, Disp1.pin_7
  N14: Part1.D5_PWM, Disp1.pin1
  N15: Part1.D6_PWM, Disp1.pin_12
  N16: Part1.D7, Disp1.pin_8
