# Fritzing sketch id2348_Schema_RGB_0 (saved by Fritzing 0.8.5b)
breadboards: 1

parts:
  Componente1 = Arduino Mega 2560 (Rev3)
  LED1 = RGB LED (com. anode, rbg) [package="5 mm [THT]"]
  R1 = Resistor [tolerance=±5% resistance=330 package=THT]
  R2 = Resistor [tolerance=±5% resistance=330 package=THT]
  R3 = Resistor [tolerance=±5% resistance=330 package=THT]
  S1 = Pushbutton [package="[THT]"]
  S2 = Pushbutton [package="[THT]"]
  R5 = Resistor [tolerance=±5% resistance=100k package=THT]
  S3 = Pushbutton [package="[THT]"]
  R7 = Resistor [tolerance=±5% resistance=100k package=THT]
  R8 = Resistor [tolerance=±5% resistance=100k package=THT]
  R9 = Trimmer Potentiometer [maximum_resistance=10kΩ package=THT]

nets:
  N1: Componente1.A0, R9.wiper
  N2: Componente1.GND, LED1.blue_cathode, R5.Pin_0, R7.Pin_0, R8.Pin_0, R9.leg2
  N3: Componente1.D10_PWM, R3.Pin_0
  N4: Componente1.D9_PWM, R2.Pin_0
  N5: Componente1.D8_PWM, R1.Pin_0
  N6: Componente1.VIN, Componente1.D5_PWM, Componente1.D6_PWM, Componente1.D7_PWM, S1.Pin_3, S1.Pin_4, S2.Pin_3, S2.Pin_4, S3.Pin_3, S3.Pin_4, R9.leg1
  N7: LED1.red_cathode, R3.Pin_1
  N8: LED1.common_anode, R2.Pin_1
  N9: LED1.green_cathode, R1.Pin_1
  N10: S1.Pin_1, S1.Pin_2, R8.Pin_1
  N11: S2.Pin_1, S2.Pin_2, R7.Pin_1
  N12: R5.Pin_1, S3.Pin_1, S3.Pin_2
