# Fritzing sketch id2349_led_rgb_con_fotoresistenze_0 (saved by Fritzing 0.9.2b)
breadboards: 1

parts:
  R2 = Resistor [tolerance=±5% resistance=220 package=THT]
  R3 = Resistor [tolerance=±5% resistance=220 package=THT]
  R4 = Photocell (LDR) [package=THT]
  R5 = Photocell (LDR) [package=THT]
  R6 = Photocell (LDR) [package=THT]
  R7 = Resistor [tolerance=±5% resistance=10k package=THT]
  R8 = Resistor [tolerance=±5% resistance=10k package=THT]
  R9 = Resistor [tolerance=±5% resistance=10k package=THT]
  R10 = Resistor [tolerance=±5% resistance=220 package=THT]
  LED1 = RGB LED (com. anode, rbg) [package="5 mm [THT]"]
  Componente1 = Arduino Uno (Rev3)

nets:
  N1: R2.Pin_0, Componente1.D10_PWM/SS
  N2: R2.Pin_1, LED1.common_anode
  N3: R3.Pin_0, Componente1.D9_PWM
  N4: R3.Pin_1, LED1.red_cathode
  N5: R4.pin_0, R8.Pin_1, Componente1.A2
  N6: R4.pin_1, R5.pin_1, R6.pin_1, Componente1.5V
  N7: R5.pin_0, R9.Pin_1, Componente1.A1
  N8: R6.pin_0, R7.Pin_1, Componente1.A0
  N9: R7.Pin_0, R8.Pin_0, R9.Pin_0, LED1.blue_cathode, Componente1.GND
  N10: R10.Pin_0, Componente1.D11_PWM/MOSI
  N11: R10.Pin_1, LED1.green_cathode

notes:
  3 resistenze da 220 ohm
  3 resitenze da 10 k ohm
  1 led rgb
  arduino uno rev 3
  jumper
