# Fritzing sketch id234_7.1_0 (saved by Fritzing 0.8.7b)
breadboards: 1

parts:
  Part1 = Arduino Uno (Rev3)
  Power_plug1 = Power plug
  S1 = Pushbutton [package="[THT]"]
  R1 = Resistor [tolerance=±5% resistance=10k package=THT]
  IC4 = H-Bridge [part_number=Relay package=THT]
  U6 = Optocoupler [package=THT]
  R2 = Resistor [tolerance=±5% resistance=100 package=THT]
  D4 = Rectifier Diode [part_number=1N4001 package="300 mil [THT]"]  # not connected

nets:
  N1: Part1.D11_PWM/MOSI, S1.Pin_3, S1.Pin_4, R1.Pin_0
  N2: Part1.D12/MISO, R2.Pin_0
  N3: Part1.GND, S1.Pin_1, S1.Pin_2, U6.Pin_2
  N4: Part1.5V, R1.Pin_1
  N5: Power_plug1.GND, IC4.VCC1
  N6: Power_plug1.VCC, U6.Pin_5
  N7: IC4.1_2EN, U6.Pin_4
  N8: U6.Pin_1, R2.Pin_1
