# Fritzing sketch id2350_Led_RGB_con_Potenciometro_0 (saved by Fritzing 0.9.2b)
breadboards: 1

parts:
  Parte1 = Arduino Uno (Rev3)
  R1 = Resistor [tolerance=±0.1% resistance=220 package=THT]
  LED1 = RGB LED (com. cathode, rgb) [package="5 mm [THT]"]
  R4 = Trimmer Potentiometer [maximum_resistance=10kΩ package=THT]

nets:
  N1: Parte1.A0, R4.wiper
  N2: Parte1.D8, LED1.blue_anode
  N3: Parte1.D9_PWM, LED1.green_anode
  N4: Parte1.D10_PWM/SS, LED1.red_anode
  N5: Parte1.5V, R4.leg2
  N6: R1.Pin_0, R4.leg1
  N7: R1.Pin_1, LED1.common_cathode
