# Fritzing sketch id2351_Mood_Light_V1.0_0 (saved by Fritzing 0.7.11b)
breadboards: 1

parts:
  ATMega328 = atmega328 [package=dip]
  IC1 = ULN2003A [package="DIP16 [THT]"]
  IC2 = ULN2003A [package="DIP16 [THT]"]
  Crystal = Crystal [package=THT]
  C1 = Tantalum Capacitor [package=THT]
  C2 = Tantalum Capacitor [package=THT]

nets:
  N1: ATMega328.D2, IC1.In_7
  N2: ATMega328.D3_(PWM), IC1.In_6
  N3: ATMega328.D4, IC1.In_5
  N4: ATMega328.VCC, ATMega328.AVCC
  N5: ATMega328.GND, C1.-, C2.-
  N6: ATMega328.XLAT1, Crystal.pin_1, C2.+
  N7: ATMega328.XLAT2, Crystal.pin_0, C1.+
  N8: ATMega328.D5_(PWM), IC1.In_4
  N9: ATMega328.D6_(PWM), IC1.In_3
  N10: ATMega328.D7, IC1.In_2
  N11: ATMega328.D8, IC2.In_7
  N12: ATMega328.D9_(PWM), IC2.In_6
  N13: ATMega328.D10_(PWM), IC2.In_5
  N14: ATMega328.D11_(PWM), IC2.In_4
  N15: ATMega328.D12, IC2.In_3
  N16: ATMega328.D13, IC2.In_2

notes:
  GND
  5V
  Tx
  Rx
  ATMega
  Crystal
  C1-2 10µF
  ULN2003A
  Ch 1
  Ch 2
  Ch 3
  Ch 4
  .
  Mood Light V1.0
  Jelle T.
  Robbert B.
  Raf V.
