# Fritzing sketch id2355_LED_showdown_0 (saved by Fritzing 0.9.3b)
breadboards: 1

parts:
  Part1 = Arduino Uno (Rev3)
  LED1 = LED - 5mm [color="Red (633nm)" package="5 mm [THT]"]
  LED2 = smd LED [color="Red (633nm)" package="1206 [SMD]"]
  LED3 = smd LED [color="Red (633nm)" package="0603 [SMD]"]

nets:
  N1: Part1.D2, LED1.anode
  N2: Part1.D3_PWM, LED2.anode
  N3: Part1.D4, LED3.anode
  N4: LED1.cathode, LED2.cathode, LED3.cathode
