# Fritzing sketch id2356_ledstrip_0 (saved by Fritzing 0.8.5b)
breadboards: 1

parts:
  VCC1 = Battery block 9V
  Part1 = Arduino Uno (Rev3)
  C1 = Capacitor Polarized [package=panasonic_g]
  RGB_SMD_LED1 = SMD RGB LED (WS2812) [package=5050]
  R1 = Resistor [tolerance=±5% resistance=220 package=THT]

nets:
  GND: VCC1.-, Part1.GND, C1.-, RGB_SMD_LED1.VSS
  N1: VCC1.+, C1.+, RGB_SMD_LED1.VCC
  N2: Part1.D4, R1.Pin_1
  N3: RGB_SMD_LED1.DIn, R1.Pin_0
