# Fritzing sketch id2357_TrippyShadez_v1_0 (saved by Fritzing 0.9.3b)
circuit board: 12.9816cm x 3.93697cm
circuit board: 12.9672cm x 3.92681cm
circuit board: 14.6253cm x 5.10032cm
breadboards: 1

parts:
  Part1 = ws2812b [package="smd 2812b"]
  Part2 = ws2812b [package="smd 2812b"]
  Part3 = ws2812b [package="smd 2812b"]
  Part4 = ws2812b [package="smd 2812b"]
  Part5 = ws2812b [package="smd 2812b"]
  Part6 = ws2812b [package="smd 2812b"]
  Part7 = ws2812b [package="smd 2812b"]
  Part8 = ws2812b [package="smd 2812b"]
  Part9 = ws2812b [package="smd 2812b"]
  Part10 = ws2812b [package="smd 2812b"]
  Part11 = ws2812b [package="smd 2812b"]
  Part12 = ws2812b [package="smd 2812b"]
  Part13 = ws2812b [package="smd 2812b"]
  Button_to_MC = rounded female pin header, 1 pin [form="♀ (female rounded)"]
  led8 = ws2812b [package="smd 2812b"]
  Led1 = ws2812b [package="smd 2812b"]
  led2 = ws2812b [package="smd 2812b"]
  led9 = ws2812b [package="smd 2812b"]
  led10 = ws2812b [package="smd 2812b"]
  led3 = ws2812b [package="smd 2812b"]
  led11 = ws2812b [package="smd 2812b"]
  led4 = ws2812b [package="smd 2812b"]
  led12 = ws2812b [package="smd 2812b"]
  led5 = ws2812b [package="smd 2812b"]
  led6 = ws2812b [package="smd 2812b"]
  led13 = ws2812b [package="smd 2812b"]
  led7 = ws2812b [package="smd 2812b"]
  RightArm_to_Front = female pin header, 4 pins [form="♀ (female)"]
  button = Pushbutton [package="[SMD]"]
  LeftArm_to_Front = female pin header, 4 pins [form="♀ (female)"]
  l1 = ws2812b [package="smd 2812b"]
  RightArm_to_Front1 = female pin header, 4 pins [form="♀ (female)"]
  LeftArm_to_Front1 = female pin header, 4 pins [form="♀ (female)"]
  l2 = ws2812b [package="smd 2812b"]
  l4 = ws2812b [package="smd 2812b"]
  l3 = ws2812b [package="smd 2812b"]
  l5 = ws2812b [package="smd 2812b"]
  l10 = ws2812b [package="smd 2812b"]
  l14 = ws2812b [package="smd 2812b"]
  l13 = ws2812b [package="smd 2812b"]
  l11 = ws2812b [package="smd 2812b"]
  l12 = ws2812b [package="smd 2812b"]
  l6 = ws2812b [package="smd 2812b"]
  l7 = ws2812b [package="smd 2812b"]
  l8 = ws2812b [package="smd 2812b"]
  l9 = ws2812b [package="smd 2812b"]
  l18 = ws2812b [package="smd 2812b"]
  l15 = ws2812b [package="smd 2812b"]
  l17 = ws2812b [package="smd 2812b"]
  l16 = ws2812b [package="smd 2812b"]
  ll36 = ws2812b [package="smd 2812b"]
  ll31 = ws2812b [package="smd 2812b"]
  ll24 = ws2812b [package="smd 2812b"]
  ll23 = ws2812b [package="smd 2812b"]
  ll21 = ws2812b [package="smd 2812b"]
  ll25 = ws2812b [package="smd 2812b"]
  ll28 = ws2812b [package="smd 2812b"]
  ll20 = ws2812b [package="smd 2812b"]
  ll33 = ws2812b [package="smd 2812b"]
  ll22 = ws2812b [package="smd 2812b"]
  ll29 = ws2812b [package="smd 2812b"]
  ll19 = ws2812b [package="smd 2812b"]
  ll27 = ws2812b [package="smd 2812b"]
  ll32 = ws2812b [package="smd 2812b"]
  ll30 = ws2812b [package="smd 2812b"]
  ll35 = ws2812b [package="smd 2812b"]
  ll26 = ws2812b [package="smd 2812b"]
  ll34 = ws2812b [package="smd 2812b"]
  MC_connector = female pin header, 3 pins [form="♀ (female)"]
  Expansion_to_MC = rounded female pin header, 1 pin [form="♀ (female rounded)"]
  Mic_attachment = rounded female pin header, 3 pins [form="♀ (female rounded)"]

nets:
  VDD: Part1.VDD, Part2.VDD, Part3.VDD, Part4.VDD, Part5.VDD, Part6.VDD, Part7.VDD, Part8.VDD, Part9.VDD, Part10.VDD, Part11.VDD, Part12.VDD, Part13.VDD, LeftArm_to_Front.pin2, MC_connector.pin1, Mic_attachment.pin3
  N1: Part1.DOUT, Part2.DIN
  VSS: Part1.VSS, Part2.VSS, Part3.VSS, Part4.VSS, Part5.VSS, Part6.VSS, Part7.VSS, Part8.VSS, Part9.VSS, Part10.VSS, Part11.VSS, Part12.VSS, Part13.VSS, LeftArm_to_Front.pin3, MC_connector.pin2, Mic_attachment.pin2
  N2: Part1.DIN, MC_connector.pin3
  N3: Part2.DOUT, Part3.DIN
  N4: Part3.DOUT, Part4.DIN
  N5: Part4.DOUT, Part5.DIN
  N6: Part5.DOUT, Part6.DIN
  N7: Part6.DOUT, Part7.DIN
  N8: Part7.DOUT, Part8.DIN
  N9: Part8.DOUT, Part9.DIN
  N10: Part9.DOUT, Part10.DIN
  N11: Part10.DOUT, Part11.DIN
  N12: Part11.DOUT, Part12.DIN
  N13: Part12.DOUT, Part13.DIN
  N14: Part13.DOUT, LeftArm_to_Front.pin4
  N15: Button_to_MC.pin1, LeftArm_to_Front.pin1
  VDD_2: led8.VDD, Led1.VDD, led2.VDD, led9.VDD, led10.VDD, led3.VDD, led11.VDD, led4.VDD, led12.VDD, led5.VDD, led6.VDD, led13.VDD, led7.VDD, RightArm_to_Front.pin2
  N16: led8.DOUT, led9.DIN
  VSS_2: led8.VSS, Led1.VSS, led2.VSS, led9.VSS, led10.VSS, led3.VSS, led11.VSS, led4.VSS, led12.VSS, led5.VSS, led6.VSS, led13.VSS, led7.VSS, RightArm_to_Front.pin3, button.Pin_1, button.Pin_2
  N17: led8.DIN, led7.DOUT
  N18: Led1.DOUT, led2.DIN
  N19: Led1.DIN, RightArm_to_Front.pin4
  N20: led2.DOUT, led3.DIN
  N21: led9.DOUT, led10.DIN
  N22: led10.DOUT, led11.DIN
  N23: led3.DOUT, led4.DIN
  N24: led11.DOUT, led12.DIN
  N25: led4.DOUT, led5.DIN
  N26: led12.DOUT, led13.DIN
  N27: led5.DOUT, led6.DIN
  N28: led6.DOUT, led7.DIN
  N29: RightArm_to_Front.pin1, button.Pin_3, button.Pin_4
  VDD_3: l1.VDD, RightArm_to_Front1.pin2, LeftArm_to_Front1.pin2, l2.VDD, l4.VDD, l3.VDD, l5.VDD, l10.VDD, l14.VDD, l13.VDD, l11.VDD, l12.VDD, l6.VDD, l7.VDD, l8.VDD, l9.VDD, l18.VDD, l15.VDD, l17.VDD, l16.VDD, ll36.VDD, ll31.VDD, ll24.VDD, ll23.VDD, ll21.VDD, ll25.VDD, ll28.VDD, ll20.VDD, ll33.VDD, ll22.VDD, ll29.VDD, ll19.VDD, ll27.VDD, ll32.VDD, ll30.VDD, ll35.VDD, ll26.VDD, ll34.VDD
  N30: l1.DOUT, l2.DIN
  VSS_3: l1.VSS, RightArm_to_Front1.pin3, LeftArm_to_Front1.pin3, l2.VSS, l4.VSS, l3.VSS, l5.VSS, l10.VSS, l14.VSS, l13.VSS, l11.VSS, l12.VSS, l6.VSS, l7.VSS, l8.VSS, l9.VSS, l18.VSS, l15.VSS, l17.VSS, l16.VSS, ll36.VSS, ll31.VSS, ll24.VSS, ll23.VSS, ll21.VSS, ll25.VSS, ll28.VSS, ll20.VSS, ll33.VSS, ll22.VSS, ll29.VSS, ll19.VSS, ll27.VSS, ll32.VSS, ll30.VSS, ll35.VSS, ll26.VSS, ll34.VSS
  N31: l1.DIN, LeftArm_to_Front1.pin4
  N32: RightArm_to_Front1.pin1, LeftArm_to_Front1.pin1
  N33: RightArm_to_Front1.pin4, ll36.DOUT
  N34: l2.DOUT, l3.DIN
  N35: l4.DOUT, l5.DIN
  N36: l4.DIN, l3.DOUT
  N37: l5.DOUT, l6.DIN
  N38: l10.DOUT, l11.DIN
  N39: l10.DIN, l9.DOUT
  N40: l14.DOUT, l15.DIN
  N41: l14.DIN, l13.DOUT
  N42: l13.DIN, l12.DOUT
  N43: l11.DOUT, l12.DIN
  N44: l6.DOUT, l7.DIN
  N45: l7.DOUT, l8.DIN
  N46: l8.DOUT, l9.DIN
  N47: l18.DOUT, ll19.DIN
  N48: l18.DIN, l17.DOUT
  N49: l15.DOUT, l16.DIN
  N50: l17.DIN, l16.DOUT
  N51: ll36.DIN, ll35.DOUT
  N52: ll31.DOUT, ll32.DIN
  N53: ll31.DIN, ll30.DOUT
  N54: ll24.DOUT, ll25.DIN
  N55: ll24.DIN, ll23.DOUT
  N56: ll23.DIN, ll22.DOUT
  N57: ll21.DOUT, ll22.DIN
  N58: ll21.DIN, ll20.DOUT
  N59: ll25.DOUT, ll26.DIN
  N60: ll28.DOUT, ll29.DIN
  N61: ll28.DIN, ll27.DOUT
  N62: ll20.DIN, ll19.DOUT
  N63: ll33.DOUT, ll34.DIN
  N64: ll33.DIN, ll32.DOUT
  N65: ll29.DOUT, ll30.DIN
  N66: ll27.DIN, ll26.DOUT
  N67: ll35.DIN, ll34.DOUT
  N68: Expansion_to_MC.pin1, Mic_attachment.pin1

notes:
  test
  d
  g
  v
  b
  TrippyShadez
