# Fritzing sketch id2358_SunriseLEDStrip_0 (saved by Fritzing 0.9.3b)
breadboards: 1

parts:
  Power_plug1 = Power plug
  Part1 = Photon  # not connected
  LPD8806_RGB_LED_Strip = LPD8806_RGB_LED_Strip

nets:
  N1: Power_plug1.VCC, LPD8806_RGB_LED_Strip.connector3
  N2: Power_plug1.GND, LPD8806_RGB_LED_Strip.connector0
