# Fritzing sketch id2359_oneLED_0 (saved by Fritzing 0.9.3b)
breadboards: 1

parts:
  S1 = Pushbutton [package="[THT]"]
  VCC1 = Battery
  LED1 = LED - 5mm [color="Red (633nm)" package="5 mm [THT]"]
  R1 = Resistor [tolerance=±5% resistance=220 package="2512 [SMD]"]

nets:
  N1: S1.Pin_1, S1.Pin_2, LED1.cathode
  N2: S1.Pin_3, S1.Pin_4, VCC1.+
  N3: VCC1.-, R1.Pin_1
  N4: LED1.anode, R1.Pin_0
