# Fritzing sketch id2360_LED_Traffic_Light2_0 (saved by Fritzing 0.9.0b)
breadboards: 1

parts:
  Part1 = Arduino Uno (Rev3)
  LED1 = LED - 5mm [color="Green (565nm)" package="5 mm [THT]"]
  R1 = Resistor [tolerance=±5% resistance=220 package=THT]
  LED2 = LED - 5mm [color="Yellow (595nm)" package="5 mm [THT]"]
  LED3 = LED - 5mm [color="Red (633nm)" package="5 mm [THT]"]
  R2 = Resistor [tolerance=±5% resistance=220 package=THT]
  R3 = Resistor [tolerance=±5% resistance=220 package=THT]

nets:
  N1: Part1.D8, LED2.anode
  N2: Part1.D12/MISO, LED1.anode
  N3: Part1.GND, R1.Pin_0, R2.Pin_0, R3.Pin_0
  N4: LED1.cathode, R3.Pin_1
  N5: R1.Pin_1, LED3.cathode
  N6: LED2.cathode, R2.Pin_1
