# Fritzing sketch id2361_LED_Transistor_Switcher_0 (saved by Fritzing 0.7.7b)
breadboards: 1

parts:
  Q1 = NPN-Transistor [package="TO92 [THT]"]
  R1 = Resistor [tolerance=±5% resistance=220 package=THT]
  LED1 = LED - 5mm [color="Red (633nm)" package="5 mm [THT]"]
  Arduino1 = Arduino
  VCC1 = Battery block 9V
  R2 = Resistor [tolerance=±5% resistance=220 package=THT]

nets:
  N1: Q1.E, LED1.cathode
  N2: Q1.B, R2.Pin_0
  N3: Q1.C, Arduino1.GND
  N4: R1.Pin_0, VCC1.+
  N5: R1.Pin_1, LED1.anode
  N6: Arduino1.D5, R2.Pin_1
