# Fritzing sketch id2362_Kamashi_Loader2_0 (saved by Fritzing 0.9.3b)
circuit board: 4.2cm x 5cm
breadboards: 1

parts:
  LED1 = LED - 5mm [color="Red (633nm)" package="5 mm [THT]"]
  LED2 = LED - 5mm [color="Red (633nm)" package="5 mm [THT]"]
  LED3 = LED - 5mm [color="Red (633nm)" package="5 mm [THT]"]
  LED4 = LED - 5mm [color="Red (633nm)" package="5 mm [THT]"]
  LED5 = LED - 5mm [color="Red (633nm)" package="5 mm [THT]"]
  LED7 = LED - 5mm [color="Red (633nm)" package="5 mm [THT]"]
  R1 = Resistor [tolerance=±5% resistance=100 package=THT]
  R2 = Resistor [tolerance=±5% resistance=100 package=THT]
  R3 = Resistor [tolerance=±5% resistance=100 package=THT]
  R4 = Resistor [tolerance=±5% resistance=100 package=THT]
  R5 = Resistor [tolerance=±5% resistance=100 package=THT]
  R6 = Resistor [tolerance=±5% resistance=100 package=THT]
  R7 = Resistor [tolerance=±5% resistance=100 package=THT]
  Pad1 = Pad [width=3.1513710862056716 height=2.7916848595269452 connect=center]
  Pad2 = Pad [width=3.1513710862056716 height=2.7916848595269452 connect=center]
  LED6 = LED - 5mm [color="Red (633nm)" package="5 mm [THT]"]
  S1 = Taiway 100-SP-X-T1 SPDT Miniature Toggle Switch [part_number=100-SP-X-T1-0-0-B1-M2 package=THT]

nets:
  N1: LED1.cathode, R1.Pin_0
  N2: LED1.anode, LED2.anode, LED3.anode, LED4.anode, LED5.anode, LED6.anode, S1.L2
  N3: LED2.cathode, R2.Pin_0
  N4: LED3.cathode, R3.Pin_0
  N5: LED4.cathode, R4.Pin_0
  N6: LED5.cathode, R5.Pin_0
  N7: LED7.cathode, R7.Pin_0
  N8: LED7.anode, S1.L1
  GND: R1.Pin_1, R2.Pin_1, R3.Pin_1, R4.Pin_1, R5.Pin_1, R6.Pin_1, R7.Pin_1, Pad2.pad
  N9: R6.Pin_0, LED6.cathode
  VCC: Pad1.pad, S1.COM

notes:
  GP Battery, Kamashi Loader2, 0
