# Fritzing sketch id2368_LED_Button_0 (saved by Fritzing 0.9.0b)
breadboards: 1

parts:
  Raspberry_Pi1 = Raspberry Pi B rev2
  S1 = Momentary Switch [package=ksa_sealed_tac_switch]
  LED1 = smd LED [color="Red (633nm)" package="1206 [SMD]"]
  R1 = Resistor [tolerance=±5% resistance=1 package="1206 [SMD]"]

nets:
  N1: Raspberry_Pi1.3V3, S1.3, S1.4
  N2: Raspberry_Pi1.GND, R1.Pin_1
  N3: S1.1, S1.2, LED1.cathode
  N4: LED1.anode, R1.Pin_0
