# Fritzing sketch id2369_clock_0 (saved by Fritzing 0.8.3b)
perfboards: 1

parts:
  U6 = MAX7219 [package=dil24]  # not connected
  U7 = MAX7219 [package=dil24]  # not connected
  S2 = Pushbutton [package="[THT]"]
  U8 = atmega328  # not connected
  S3 = Pushbutton [package="[THT]"]
  S4 = Pushbutton [package="[THT]"]
  S5 = Pushbutton [package="[THT]"]
  U9 = 74HC595 [package="DIP16 [THT]"]  # not connected
  U10 = 74HC595 [package="DIP16 [THT]"]  # not connected
  U11 = 74HC595 [package="DIP16 [THT]"]  # not connected
  U12 = 74HC595 [package="DIP16 [THT]"]  # not connected
  R1 = Resistor [tolerance=±5% resistance=180 package=THT]  # not connected
  R2 = Resistor [tolerance=±5% resistance=180 package=THT]  # not connected
  R3 = Resistor [tolerance=±5% resistance=180 package=THT]  # not connected
  R4 = Resistor [tolerance=±5% resistance=180 package=THT]  # not connected
  R5 = Resistor [tolerance=±5% resistance=180 package=THT]  # not connected
  R6 = Resistor [tolerance=±5% resistance=180 package=THT]  # not connected
  R7 = Resistor [tolerance=±5% resistance=180 package=THT]  # not connected
  R8 = Resistor [tolerance=±5% resistance=180 package=THT]  # not connected
  R9 = Resistor [tolerance=±5% resistance=180 package=THT]  # not connected
  R10 = Resistor [tolerance=±5% resistance=180 package=THT]  # not connected
  R11 = Resistor [tolerance=±5% resistance=100 package=THT]  # not connected
  R12 = Resistor [tolerance=±5% resistance=100 package=THT]  # not connected
  R13 = Resistor [tolerance=±5% resistance=100 package=THT]  # not connected
  R14 = Resistor [tolerance=±5% resistance=100 package=THT]  # not connected
  R15 = Resistor [tolerance=±5% resistance=100 package=THT]  # not connected
  R16 = Resistor [tolerance=±5% resistance=100 package=THT]  # not connected
  R17 = Resistor [tolerance=±5% resistance=100 package=THT]  # not connected
  R18 = Resistor [tolerance=±5% resistance=100 package=THT]  # not connected
  R19 = Resistor [tolerance=±5% resistance=100 package=THT]  # not connected
  R20 = Resistor [tolerance=±5% resistance=100 package=THT]  # not connected
  R21 = Resistor [tolerance=±5% resistance=100 package=THT]  # not connected
  R22 = Resistor [tolerance=±5% resistance=100 package=THT]  # not connected
  R23 = Resistor [tolerance=±5% resistance=100 package=THT]  # not connected
  R24 = Resistor [tolerance=±5% resistance=100 package=THT]  # not connected
  R25 = Resistor [tolerance=±5% resistance=100 package=THT]  # not connected
  R26 = Resistor [tolerance=±5% resistance=100 package=THT]  # not connected
  R27 = Resistor [tolerance=±5% resistance=100 package=THT]  # not connected
  R28 = Resistor [tolerance=±5% resistance=100 package=THT]  # not connected
  R29 = Resistor [tolerance=±5% resistance=100 package=THT]  # not connected
  R30 = Resistor [tolerance=±5% resistance=100 package=THT]  # not connected
  R32 = Resistor [tolerance=±5% resistance=1k package=THT]
  R33 = Resistor [tolerance=±5% resistance=1k package=THT]
  R34 = Resistor [tolerance=±5% resistance=1k package=THT]
  R31 = Resistor [tolerance=±1% resistance=1k package=THT]
  IC1 = DS1307 [package=THT]  # not connected
  Part1 = LilyPad Coin Cell Battery Holder  # not connected
  U13 = DS18B20  # not connected
  LDR1 = LDR - GL5528  # not connected

nets:
  N1: S2.Pin_1, S2.Pin_2, S3.Pin_1, S3.Pin_2, S4.Pin_1, S4.Pin_2, S5.Pin_1, S5.Pin_2
  N2: S2.Pin_3, S2.Pin_4
  N3: S3.Pin_3, S3.Pin_4
  N4: S4.Pin_3, S4.Pin_4
  N5: S5.Pin_3, S5.Pin_4
  N6: R32.Pin_0, R33.Pin_1
  N7: R32.Pin_1, R31.Pin_0
  N8: R33.Pin_0, R34.Pin_1
