# Fritzing sketch id2371_led_y_pulsador_0 (saved by Fritzing 0.9.3b)
breadboards: 1

parts:
  LED1 = LED - 5mm [color="Red (633nm)" package="5 mm [THT]"]
  S2 = Pushbutton [package="[THT]"]
  R1 = Resistor [tolerance=±5% resistance=220 package=THT]
  R2 = Resistor [tolerance=±5% resistance=220 package=THT]
  Componente1 = Arduino Uno (Rev3)

nets:
  N1: LED1.cathode, R2.Pin_1
  N2: LED1.anode, Componente1.D5_PWM
  N3: S2.Pin_1, S2.Pin_2, Componente1.5V
  N4: S2.Pin_3, S2.Pin_4, R1.Pin_1, Componente1.D6_PWM
  N5: R1.Pin_0, R2.Pin_0, Componente1.GND
