# Fritzing sketch id2372_fritz_led_0 (saved by Fritzing 0.9.1b)
breadboards: 1

parts:
  Parte1 = Arduino Uno (Rev3)
  LED1 = LED - 5mm [color="Red (633nm)" package="5 mm [THT]"]
  R1 = Resistor [tolerance=±5% resistance=220 package=THT]
  LED2 = LED - 5mm [color="Green (565nm)" package="5 mm [THT]"]
  R2 = Resistor [tolerance=±5% resistance=220 package=THT]
  LED3 = LED - 5mm [color="Orange (620nm)" package="5 mm [THT]"]
  R3 = Resistor [tolerance=±5% resistance=220 package=THT]
  LED4 = LED - 5mm [color="Yellow (592nm)" package="5 mm [THT]"]
  R4 = Resistor [tolerance=±5% resistance=220 package=THT]

nets:
  N1: Parte1.D10_PWM/SS, R3.Pin_1
  N2: Parte1.D11_PWM/MOSI, R4.Pin_1
  N3: Parte1.D12/MISO, R2.Pin_1
  N4: Parte1.D13/SCK, R1.Pin_1
  N5: Parte1.GND, LED1.cathode, LED2.cathode, LED3.cathode, LED4.cathode
  N6: LED1.anode, R1.Pin_0
  N7: LED2.anode, R2.Pin_0
  N8: LED3.anode, R3.Pin_0
  N9: LED4.anode, R4.Pin_0
