# Fritzing sketch id2373_LED555_0 (saved by Fritzing 0.9.3b)
breadboards: 1

parts:
  LED1 = LED - 5mm [color="Red (633nm)" package="5 mm [THT]"]
  C1 = Electrolytic Capacitor [capacitance=100µF package="100 mil [THT, electrolytic]"]
  U1 = 555 Timer [package="DIP8 [THT]"]
  R1 = Resistor [tolerance=±5% resistance=560 package=THT]
  R2 = Resistor [tolerance=±5% resistance=330 package=THT]

nets:
  N1: LED1.cathode, C1.-, U1.Ground
  N2: LED1.anode, U1.Output
  N3: C1.+, U1.Trigger, U1.Threshold, R2.Pin_1
  N4: U1.Reset, U1.Vcc_Supply_Voltage, R1.Pin_0
  N5: U1.Discharge, R1.Pin_1, R2.Pin_0
