# Fritzing sketch id2374_seven_segment_01_0 (saved by Fritzing 0.9.1b)
breadboards: 1

parts:
  U1 = 7-SEGMENT-DISPLAY [package=7-segment-display]
  R1 = Resistor [tolerance=±5% resistance=220 package=THT]
  R2 = Resistor [tolerance=±5% resistance=220 package=THT]
  R3 = Resistor [tolerance=±5% resistance=220 package=THT]
  R4 = Resistor [tolerance=±5% resistance=220 package=THT]
  R5 = Resistor [tolerance=±5% resistance=220 package=THT]
  R6 = Resistor [tolerance=±5% resistance=220 package=THT]
  R7 = Resistor [tolerance=±5% resistance=220 package=THT]
  R8 = Resistor [tolerance=±5% resistance=220 package=THT]
  Componente1 = Arduino Mega 2560 (Rev3)

nets:
  N1: U1.E, R3.Pin_0
  N2: U1.D, R5.Pin_0
  N3: U1.G1, R6.Pin_0
  N4: U1.C, U1.F, Componente1.GND
  N5: U1.DP, R7.Pin_0
  N6: U1.B, R8.Pin_0
  N7: U1.A, R4.Pin_0
  N8: U1.G2, R2.Pin_0
  N9: U1.G, R1.Pin_0
  N10: R1.Pin_1, Componente1.D8_PWM
  N11: R2.Pin_1, Componente1.D11_PWM
  N12: R3.Pin_1, Componente1.D7_PWM
  N13: R4.Pin_1, Componente1.D12_PWM
  N14: R5.Pin_1, Componente1.D5_PWM
  N15: R6.Pin_1, Componente1.D4_PWM
  N16: R7.Pin_1, Componente1.D3_PWM
  N17: R8.Pin_1, Componente1.D2_PWM
