# Fritzing sketch id2375_Blink_0 (saved by Fritzing 0.8.7b)
circuit board: 8.46667cm x 5.64444cm
breadboards: 1

parts:
  Part1 = Arduino Uno (Rev3)
  R1 = Resistor [tolerance=±5% resistance=220 package=THT]
  LED1 = LED - 5mm [color="Red (633nm)" package="5 mm [THT]"]

nets:
  N1: Part1.D12/MISO, R1.Pin_1
  N2: Part1.GND, LED1.cathode
  N3: R1.Pin_0, LED1.anode
