# Fritzing sketch id2377_Led_Blink_test_0 (saved by Fritzing 0.9.2b)
circuit board: 5.57232cm x 5.3195cm
breadboards: 1

parts:
  Bottone1 = Pushbutton [package="[THT]"]
  Bottone2 = Pushbutton [package="[THT]"]
  LED1 = LED - 5mm [color="Green (560nm)" package="5 mm [THT]"]
  LED2 = LED - 5mm [color="Red (633nm)" package="5 mm [THT]"]
  J1 = Piezo Speaker
  R1 = Resistor [tolerance=±5% resistance=330 package=THT]
  R2 = Resistor [tolerance=±5% resistance=330 package=THT]
  Arduino = Arduino Uno (Rev3) - ICSP

nets:
  N1: Bottone1.Pin_1, Bottone1.Pin_2, Arduino.D6_PWM
  N2: Bottone1.Pin_3, Bottone1.Pin_4, Bottone2.Pin_3, Bottone2.Pin_4, LED1.cathode, LED2.cathode, J1.pin1, Arduino.GND
  N3: Bottone2.Pin_1, Bottone2.Pin_2, Arduino.D5_PWM
  N4: LED1.anode, R1.Pin_0
  N5: LED2.anode, R2.Pin_0
  N6: J1.pin2, Arduino.D9_PWM
  N7: R1.Pin_1, Arduino.D7
  N8: R2.Pin_1, Arduino.D8
