# Fritzing sketch id2378_LED_blink_arduino_0 (saved by Fritzing 0.9.3b)
breadboards: 1

parts:
  パーツ1 = Arduino Uno (Rev3)
  R1 = Resistor [tolerance=±5% resistance=270 package=THT]
  LED1 = LED - 5mm [color="Red (633nm)" package="5 mm [THT]"]

nets:
  N1: パーツ1.D5_PWM, LED1.cathode
  N2: パーツ1.5V, R1.Pin_1
  N3: R1.Pin_0, LED1.anode
