# Fritzing sketch id2380_LED_blinker_0 (saved by Fritzing 0.9.3b)
breadboards: 1

parts:
  Bauteil1 = Arduino Nano (Rev3.0)
  LED1 = LED - 5mm [color="Red (633nm)" package="5 mm [THT]"]
  R1 = Resistor [tolerance=±5% resistance=220 package=THT]

nets:
  N1: Bauteil1.RESET, LED1.anode
  N2: Bauteil1.D9, R1.Pin_0
  N3: LED1.cathode, R1.Pin_1

notes:
  *Blink*
