# Fritzing sketch id2381_Led_Multicolor_Interr_0 (saved by Fritzing 0.9.3b)
breadboards: 1

parts:
  Componente1 = Arduino Uno (Rev3)
  S3 = Momentary Switch [package=ksa_sealed_tac_switch]
  R1_R2_R3 = Resistor [tolerance=±5% resistance=220 package=THT]
  R2 = Resistor [tolerance=±5% resistance=220 package=THT]
  R3 = Resistor [tolerance=±5% resistance=220 package=THT]
  LED_RGB_Cadoto_Comune = RGB LED (com. cathode, rgb) [package="5 mm [THT]"]
  R4 = Resistor [tolerance=±5% resistance=10k package=THT]

nets:
  N1: Componente1.D8, S3.2
  N2: Componente1.D3_PWM, R3.Pin_0
  N3: Componente1.D5_PWM, R1_R2_R3.Pin_0
  N4: Componente1.D6_PWM, R2.Pin_0
  N5: Componente1.5V, S3.3
  N6: Componente1.GND, R4.Pin_0
  N7: S3.1, R4.Pin_1
  N8: R1_R2_R3.Pin_1, LED_RGB_Cadoto_Comune.blue_anode
  N9: R2.Pin_1, LED_RGB_Cadoto_Comune.green_anode
  N10: R3.Pin_1, LED_RGB_Cadoto_Comune.red_anode
