# Fritzing sketch id2383_ledbutton_0 (saved by Fritzing 0.9.3b)

parts:
  Part1 = Arduino Uno (Rev3)
  S1 = Round Pushbutton
  S2 = Round Pushbutton
  R1 = Resistor [tolerance=±5% resistance=220 package=THT]
  R2 = Resistor [tolerance=±5% resistance=220 package=THT]
  LED1 = LED - 5mm [color="Red (633nm)" package="5 mm [THT]"]
  LED2 = LED - 5mm [color="Red (633nm)" package="5 mm [THT]"]

nets:
  N1: Part1.D8, R1.Pin_0
  N2: Part1.D9_PWM, R2.Pin_1
  N3: Part1.D11_PWM/MOSI, LED1.anode
  N4: Part1.D12/MISO, LED2.anode
  N5: Part1.GND, S1.leg0, S2.leg1, LED1.cathode, LED2.cathode
