# Fritzing sketch id2384_LEDCligno_0 (saved by Fritzing 0.9.3b)
breadboards: 1

parts:
  Composant1 = Arduino Uno (Rev3)
  LED1 = LED - 5mm [color="Red (633nm)" package="5 mm [THT]"]
  R1 = Resistor [tolerance=±5% resistance=220 package=THT]

nets:
  N1: Composant1.D12/MISO, LED1.anode
  N2: Composant1.GND, R1.Pin_1
  N3: LED1.cathode, R1.Pin_0
