# Fritzing sketch id2385_LEDCLOCK2_0 (saved by Fritzing 0.9.1b)
perfboards: 2

parts:
  R8 = Resistor [tolerance=±5% resistance=220 package=THT]
  U1 = Packages: [package=dil28-3]
  U2 = Packages: [package=dil28-3]
  U3 = Packages: [package=dil28-3]
  U4 = Packages: [package=dil28-3]
  U5 = Packages: [package=dil28-3]
  U6 = Packages: [package=dil28-3]
  U7 = Packages: [package=dil28-3]
  U8 = Packages: [package=dil28-3]
  U9 = Packages: [package=dil28-3]
  R9 = Resistor [tolerance=±5% resistance=220 package=THT]
  R10 = Resistor [tolerance=±5% resistance=220 package=THT]
  R11 = Resistor [tolerance=±5% resistance=220 package=THT]
  R12 = Resistor [tolerance=±5% resistance=220 package=THT]
  R13 = Resistor [tolerance=±5% resistance=220 package=THT]
  R14 = Resistor [tolerance=±5% resistance=220 package=THT]
  R15 = Resistor [tolerance=±5% resistance=220 package=THT]
  R16 = Resistor [tolerance=±5% resistance=220 package=THT]
  U10 = atmega328 [package=dip]
  Bauteil1 = Bluetooth Mate Silver
  DCF-77 = mystery part, 4 pins [chip_label=DCF-77]
  5V = Header 2 [package=screwterminal-3.5mm-2_lock]
  R17 = Resistor [tolerance=±5% resistance=1k package=THT]
  R18 = Resistor [tolerance=±5% resistance=1.8k package=THT]
  S1 = Pushbutton [package="[THT]"]
  JP1 = Header 8 [package=1x08_smd]
  JP2 = Header 8 [package=1x08_smd]
  J1 = AVR ISP 6 Pin [package=2x3-ns]

nets:
  N1: R8.Pin_0, U7.GND, U7.VPRG
  N2: R8.Pin_1, U7.IREF
  N3: U1.SOUT, U9.SIN
  N4: U1.GSCLK, U8.GSCLK, U9.GSCLK
  N5: U1.IREF, R13.Pin_1
  VCC: U1.VCC, U9.VCC
  N6: U1.GND, U1.VPRG, R13.Pin_0
  N7: U1.BLANK, U2.BLANK, U3.BLANK, U4.BLANK, U5.BLANK, U6.BLANK, U7.BLANK, U8.BLANK, U9.BLANK
  N8: U1.XLAT, U2.XLAT, U3.XLAT, U4.XLAT, U5.XLAT, U6.XLAT, U7.XLAT, U8.XLAT, U9.XLAT
  N9: U1.SCLK, U2.SCLK, U3.SCLK, U4.SCLK, U5.SCLK, U6.SCLK, U7.SCLK, U8.SCLK, U9.SCLK
  N10: U2.SOUT, U6.SIN
  N11: U2.GSCLK, U5.GSCLK, U6.GSCLK
  N12: U2.IREF, R10.Pin_1
  GND: U2.GND, U2.VPRG, U5.GND, U5.VPRG, R10.Pin_0, R14.Pin_0
  N13: U2.SIN, U5.SOUT
  N14: U3.SOUT, U4.SIN
  N15: U3.GSCLK, U4.GSCLK, U7.GSCLK
  N16: U3.IREF, R15.Pin_1
  N17: U3.GND, U3.VPRG, R15.Pin_0
  N18: U3.SIN, U8.SOUT
  N19: U4.SOUT, U7.SIN
  N20: U4.IREF, R16.Pin_1
  N21: U4.GND, U4.VPRG, R16.Pin_0
  N22: U5.IREF, R14.Pin_1
  N23: U5.SIN, U7.SOUT
  N24: U6.IREF, R9.Pin_1
  N25: U6.GND, U6.VPRG, R9.Pin_0
  N26: U8.IREF, R11.Pin_1
  N27: U8.GND, U8.VPRG, R11.Pin_0
  N28: U8.SIN, U9.SOUT
  N29: U9.IREF, R12.Pin_1
  N30: U9.GND, U9.VPRG, R12.Pin_0
  N31: U10.RESET, S1.Pin_1, S1.Pin_2, J1.5
  N32: U10.D0_(RX), Bauteil1.TX_5V
  N33: U10.D1_(TX), Bauteil1.RX_5V
  N34: U10.D2, DCF-77.pin3
  VCC_2: U10.VCC, U10.AVCC, Bauteil1.VCC, 5V.1, R17.Pin_1
  GND_2: U10.GND, Bauteil1.GND, 5V.2, R18.Pin_1, S1.Pin_3, S1.Pin_4
  N35: U10.D11_(PWM), J1.4
  N36: U10.D12, J1.1
  N37: U10.D13, J1.3
  N38: DCF-77.pin1, DCF-77.pin4
  N39: R17.Pin_0, R18.Pin_0
  N40: JP1.1, JP2.1
  N41: JP1.2, JP2.2
  N42: JP1.3, JP2.3
  N43: JP1.4, JP2.4
  N44: JP1.5, JP2.5
  N45: JP1.6, JP2.6
  N46: JP1.7, JP2.7

notes:
  VCC
  GND
