# Fritzing sketch id2386_LED_Controller_0 (saved by Fritzing 0.9.3b)
breadboards: 1

parts:
  Q1 = MOSFET-NCHANNEL [package=to220v]
  Q2 = MOSFET-NCHANNEL [package=to220v]
  Q3 = MOSFET-NCHANNEL [package=to220v]
  Part1 = Arduino Uno (Rev3)
  R1 = Resistor [tolerance=±5% resistance=10k package="1206 [SMD]"]
  R2 = Resistor [tolerance=±5% resistance=10k package="1206 [SMD]"]
  R3 = Resistor [tolerance=±5% resistance=10k package="1206 [SMD]"]
  VCC2 = 4 x AAA Battery Mount
  VCC3 = 4 x AAA Battery Mount
  JP1 = Header 4 [package=1x04-1mm-ra]

nets:
  N1: Q1.G, Part1.D11_PWM/MOSI, R1.Pin_1
  N2: Q1.D, JP1.2
  N3: Q1.S, Q2.S, Q3.S, Part1.GND, R1.Pin_0, R2.Pin_0, R3.Pin_0, VCC2.-
  N4: Q2.G, Part1.D10_PWM/SS, R2.Pin_1
  N5: Q2.D, JP1.3
  N6: Q3.G, Part1.D9_PWM, R3.Pin_1
  N7: Q3.D, JP1.4
  N8: VCC2.+, VCC3.-
  N9: VCC3.+, JP1.1
