# Fritzing sketch id2386_MIC_NA_ARDUINO (saved by Fritzing 0.5.0b)
breadboards: 1

parts:
  MIC1 = Microphone
  Q1 = NPN-Transistor [package="TO92 [THT]"]
  R1 = Resistor [resistance=22k package=THT]
  R2 = Resistor [resistance=3.3k package=THT]
  C1 = Electrolytic Capacitor [capacitance=100nF rated_voltage=35V package="100 mil [THT, electrolytic]"]
  R3 = Rotary Potentiometer (Large) [package=THT]
  R4 = Trimmer Potentiometer [package=THT]
  SPKR1 = Loudspeaker

nets:
  N1: MIC1.pin1, Q1.C, R1.Pin_0, R1.Pin_1, R2.Pin_0, R2.Pin_1, C1.+, R3.leg1, SPKR1.pin1, SPKR1.pin2
  N2: MIC1.pin2, Q1.B, R3.wiper
  N3: Q1.E, R4.leg1
  N4: C1.-, R4.wiper

notes:
  BLOK SHEM za mic kako spojiti na npr. vu metar ali preko ARDUINA..Treba napvaiti kalibraciju mikrofonske kapsule pomocu PROCESING PROGRAMA..
  O TOME MALO KASNIJE.
  UMJESTO UZVUCNIKA KASNIJE SE OVA SHEMA SPAJA NPR, NA VU METAR.
  O TOME TAKODJER KASNIJE. NARAVNO DA OVO NE MOZE DA POKRENE ZVUCNIK..
