# Fritzing sketch id2387_LEDcube4_0 (saved by Fritzing 0.9.0b)
circuit board: 8.9cm x 8.9cm
breadboards: 1

parts:
  Arduino_Uno = Arduino Uno (Rev3)
  Q4 = NPN-Transistor [package="TO92 [THT]"]
  Q3 = NPN-Transistor [package="TO92 [THT]"]
  Q00 = NPN-Transistor [package="TO92 [THT]"]
  Q10 = NPN-Transistor [package="TO92 [THT]"]
  Q5 = NPN-Transistor [package="TO92 [THT]"]
  Q6 = NPN-Transistor [package="TO92 [THT]"]
  Q7 = NPN-Transistor [package="TO92 [THT]"]
  Q8 = NPN-Transistor [package="TO92 [THT]"]
  Q9 = NPN-Transistor [package="TO92 [THT]"]
  Q10_2 = NPN-Transistor [package="TO92 [THT]"]
  Q11 = NPN-Transistor [package="TO92 [THT]"]
  Q12 = NPN-Transistor [package="TO92 [THT]"]
  Q13 = NPN-Transistor [package="TO92 [THT]"]
  Q14 = NPN-Transistor [package="TO92 [THT]"]
  Q15 = NPN-Transistor [package="TO92 [THT]"]
  Q16 = NPN-Transistor [package="TO92 [THT]"]
  10k = Resistor [tolerance=±5% resistance=10k package=THT]
  10k_2 = Resistor [tolerance=±5% resistance=10k package=THT]
  10k_3 = Resistor [tolerance=±5% resistance=10k package=THT]
  10k_4 = Resistor [tolerance=±5% resistance=10k package=THT]
  220 = Resistor [tolerance=±5% resistance=220 package=THT]
  220_2 = Resistor [tolerance=±5% resistance=220 package=THT]
  220_3 = Resistor [tolerance=±5% resistance=220 package=THT]
  220_4 = Resistor [tolerance=±5% resistance=220 package=THT]

nets:
  N1: Arduino_Uno.D8, 10k_2.Pin_1
  N2: Arduino_Uno.D9_PWM, 10k.Pin_1
  N3: Arduino_Uno.D10_PWM/SS, 10k_3.Pin_1
  N4: Arduino_Uno.D11_PWM/MOSI, 10k_4.Pin_1
  N5: Arduino_Uno.D0/RX, Q9.E, Q10_2.E, Q11.E, Q12.E
  N6: Arduino_Uno.D1/TX, Q13.E, Q14.E, Q15.E, Q16.E
  N7: Arduino_Uno.D2, Q5.E, Q6.E, Q7.E, Q8.E
  N8: Arduino_Uno.D3_PWM, Q4.E, Q3.E, Q00.E, Q10.E
  N9: Arduino_Uno.D4, 220_2.Pin_1
  N10: Arduino_Uno.D5_PWM, 220.Pin_1
  N11: Arduino_Uno.D6_PWM, 220_3.Pin_1
  N12: Arduino_Uno.D7, 220_4.Pin_1
  N13: Q4.B, Q5.B, Q9.B, Q13.B, 10k.Pin_0
  N14: Q3.B, Q6.B, Q10_2.B, Q14.B, 10k_2.Pin_0
  N15: Q00.B, Q8.B, Q12.B, Q16.B, 10k_3.Pin_0
  N16: Q10.B, Q7.B, Q11.B, Q15.B, 10k_4.Pin_0

notes:
  LEDcube4 Rev 1a
  2014.08.16 Matt Stum
  +
  DO NOT use the schematic view.
  I haven't figured out how to correlate it to the physical reality, given the reliance on vias for the LED cube connection.
  DO NOT use the breadboard view.
  I haven't figured out how to correlate it to the physical reality, given the reliance on vias for the LED cube connection.
