# Fritzing sketch id2387_MIC_NA_ARDUINO_1 (saved by Fritzing 0.5.0b)
breadboards: 1

parts:
  MIC1 = Microphone
  Q1 = NPN-Transistor [package="TO92 [THT]"]
  R1 = Resistor [resistance=1k package=THT]
  R2 = Resistor [resistance=3.3k package=THT]
  C1 = Electrolytic Capacitor [capacitance=100nF rated_voltage=35V package="100 mil [THT, electrolytic]"]
  R3 = Rotary Potentiometer (Large) [package=THT]
  R4 = Trimmer Potentiometer [package=THT]
  U1 = LM 358 Dual Op-Amp [package="DIP8 [THT]"]
  C2 = Ceramic Capacitor [capacitance=100nF rated_voltage=35V package="100 mil [THT, multilayer]"]
  R5 = Resistor [resistance=220 package=THT]
  U2 = LM 358 Dual Op-Amp [package="DIP8 [THT]"]
  C3 = Ceramic Capacitor [capacitance=100nF rated_voltage=35V package="100 mil [THT, multilayer]"]
  R6 = Resistor [resistance=220 package=THT]
  Arduino1 = Arduino
  C4 = Ceramic Capacitor [capacitance=100nF rated_voltage=35V package="100 mil [THT, multilayer]"]
  LED7 = Red LED - 5mm [package="5 mm [THT]"]
  LED8 = Red LED - 5mm [package="5 mm [THT]"]
  DI1 = 7-Segment LED Display [package=THT]
  DI2 = 7-Segment LED Display [package=THT]
  R7 = Resistor [resistance=220 package=THT]  # not connected
  R8 = Resistor [resistance=220 package=THT]
  R9 = Resistor [resistance=220 package=THT]
  R10 = Resistor [resistance=220 package=THT]
  R11 = Resistor [resistance=220 package=THT]
  R12 = Resistor [resistance=220 package=THT]
  R13 = Resistor [resistance=220 package=THT]
  R14 = Resistor [resistance=220 package=THT]
  R15 = Resistor [resistance=220 package=THT]
  R16 = Resistor [resistance=220 package=THT]
  LED1 = green LED - 5mm [package="5 mm [THT]"]
  LED2 = green LED - 5mm [package="5 mm [THT]"]
  LED3 = green LED - 5mm [package="5 mm [THT]"]
  LED4 = green LED - 5mm [package="5 mm [THT]"]
  LED5 = yellow LED - 5mm [package="5 mm [THT]"]
  LED6 = yellow LED - 5mm [package="5 mm [THT]"]
  U3 = atmega168 [package="DIP28 [THT]"]  # not connected

nets:
  N1: MIC1.pin1, R2.Pin_0, C1.+, R3.leg1, U1.connector7, C2.1, U2.connector7, R6.Pin_0, Arduino1.GND
  N2: MIC1.pin2, Q1.B, R1.Pin_0, R3.wiper
  N3: Q1.C, R5.Pin_0, C3.1
  N4: R1.Pin_1, R2.Pin_1
  N5: C1.-, R4.wiper
  N6: R3.leg2, Arduino1.+5V
  N7: U1.connector0, Arduino1.A0
  N8: U1.connector1, U2.connector1, Arduino1.3V3
  N9: U1.connector6, C2.0, R5.Pin_1
  N10: U2.connector0, Arduino1.A1
  N11: U2.connector3, C4.1
  N12: U2.connector4, C4.0
  N13: U2.connector6, C3.0, R6.Pin_1
  N14: Arduino1.D11, R8.Pin_0
  N15: Arduino1.D9, R16.Pin_0
  N16: Arduino1.D8, R15.Pin_0
  N17: Arduino1.D7, R14.Pin_0
  N18: Arduino1.D6, R13.Pin_0
  N19: Arduino1.D5, R12.Pin_0
  N20: Arduino1.D4, R11.Pin_0
  N21: Arduino1.D3, R10.Pin_0
  N22: Arduino1.D2, R9.Pin_0
  N23: LED7.anode, R15.Pin_1
  N24: LED8.anode, R16.Pin_1
  N25: DI1.cathodeE, DI1.cathodeD, DI1.commAnode#2, DI1.cathodeC, DI1.cathodeDP
  N26: DI1.cathodeB, DI1.cathodeA, DI1.commAnode#7, DI1.cathodeF, DI1.cathodeG
  N27: DI2.cathodeE, DI2.cathodeD, DI2.commAnode#2, DI2.cathodeC, DI2.cathodeDP
  N28: DI2.cathodeB, DI2.cathodeA, DI2.commAnode#7, DI2.cathodeF, DI2.cathodeG, R8.Pin_1
  N29: R9.Pin_1, LED1.anode
  N30: R10.Pin_1, LED2.anode
  N31: R11.Pin_1, LED3.anode
  N32: R12.Pin_1, LED4.anode
  N33: R13.Pin_1, LED5.anode
  N34: R14.Pin_1, LED6.anode

notes:
  BLOK SHEM za mic kako spojiti na npr. vu metar ali preko ARDUINA..Treba napvaiti kalibraciju mikrofonske kapsule pomocu PROCESING PROGRAMA..
  Znaci...preko mic kapsule signal ide u prvi dio za pojacanje signala, zatim signal ide na dva LM gdje PRVI LM JE ZA LDE DIODE TJ. NISKE TONOVE. A DRUGI LMA ZA 7 SEGMENT DISP ZA VISKOKE TNOVE.
  PRVA NOGICA LM-a je gore desno u kutu. kao i za drui LM.
