# Fritzing sketch id2388_01_prac_SECUENCIA_LEDS_0 (saved by Fritzing 0.9.3b)
breadboards: 1

parts:
  R1 = Resistor [tolerance=±5% resistance=220 package=THT]
  R2 = Resistor [tolerance=±5% resistance=220 package=THT]
  R3 = Resistor [tolerance=±5% resistance=220 package=THT]
  R4 = Resistor [tolerance=±5% resistance=220 package=THT]
  R5 = Resistor [tolerance=±5% resistance=220 package=THT]
  R6 = Resistor [tolerance=±5% resistance=220 package=THT]
  LED1 = LED - 5mm [color="Red (633nm)" package="5 mm [THT]"]
  LED2 = LED - 5mm [color="Red (633nm)" package="5 mm [THT]"]
  Componente1 = Arduino Uno (Rev3)
  LED3 = LED - 5mm [color="Yellow (595nm)" package="5 mm [THT]"]
  LED4 = LED - 5mm [color="Yellow (595nm)" package="5 mm [THT]"]
  LED5 = LED - 5mm [color="Green (565nm)" package="5 mm [THT]"]
  LED6 = LED - 5mm [color="Green (565nm)" package="5 mm [THT]"]

nets:
  N1: R1.Pin_0, LED1.cathode
  N2: R1.Pin_1, R2.Pin_1, R3.Pin_1, R4.Pin_1, R5.Pin_1, R6.Pin_1, Componente1.GND
  N3: R2.Pin_0, LED4.cathode
  N4: R3.Pin_0, LED6.cathode
  N5: R4.Pin_0, LED2.cathode
  N6: R5.Pin_0, LED5.cathode
  N7: R6.Pin_0, LED3.cathode
  N8: LED1.anode, Componente1.D4
  N9: LED2.anode, Componente1.D7
  N10: Componente1.D8, LED3.anode
  N11: Componente1.D9_PWM, LED5.anode
  N12: Componente1.D5_PWM, LED4.anode
  N13: Componente1.D6_PWM, LED6.anode
