# Fritzing sketch id2389_secuencia_de_leds_0 (saved by Fritzing 0.9.3b)
breadboards: 1

parts:
  LED1 = LED - 5mm [color="Red (633nm)" package="5 mm [THT]"]
  LED2 = LED - 5mm [color="Red (633nm)" package="5 mm [THT]"]
  LED3 = LED - 5mm [color="Red (633nm)" package="5 mm [THT]"]
  LED4 = LED - 5mm [color="Red (633nm)" package="5 mm [THT]"]
  LED5 = LED - 5mm [color="Red (633nm)" package="5 mm [THT]"]
  LED6 = LED - 5mm [color="Red (633nm)" package="5 mm [THT]"]
  LED7 = LED - 5mm [color="Red (633nm)" package="5 mm [THT]"]
  LED8 = LED - 5mm [color="Red (633nm)" package="5 mm [THT]"]
  R1 = Resistor [tolerance=±5% resistance=220 package=THT]
  R2 = Resistor [tolerance=±5% resistance=220 package=THT]
  R3 = Resistor [tolerance=±5% resistance=220 package=THT]
  R4 = Resistor [tolerance=±5% resistance=220 package=THT]
  R5 = Resistor [tolerance=±5% resistance=220 package=THT]
  R6 = Resistor [tolerance=±5% resistance=220 package=THT]
  R7 = Resistor [tolerance=±5% resistance=220 package=THT]
  R8 = Resistor [tolerance=±5% resistance=220 package=THT]
  Componente1 = Arduino Uno (Rev3)
  U1 = AUDIO-JACK2 [package=audio-jack-3.5mm-smd]

nets:
  N1: LED1.cathode, LED2.cathode, LED3.cathode, LED4.cathode, LED5.cathode, LED6.cathode, LED7.cathode, LED8.cathode, Componente1.GND, U1.RSH, U1.SLEEVE
  N2: LED1.anode, R8.Pin_0
  N3: LED2.anode, R7.Pin_0
  N4: LED3.anode, R6.Pin_0
  N5: LED4.anode, R5.Pin_0
  N6: LED5.anode, R4.Pin_0
  N7: LED6.anode, R3.Pin_0
  N8: LED7.anode, R2.Pin_0
  N9: LED8.anode, R1.Pin_0
  N10: R1.Pin_1, Componente1.D10_PWM/SS
  N11: R2.Pin_1, Componente1.D9_PWM
  N12: R3.Pin_1, Componente1.D8
  N13: R4.Pin_1, Componente1.D7
  N14: R5.Pin_1, Componente1.D6_PWM
  N15: R6.Pin_1, Componente1.D5_PWM
  N16: R7.Pin_1, Componente1.D4
  N17: R8.Pin_1, Componente1.D3_PWM
  N18: Componente1.A0, U1.RING
