# Fritzing sketch id2390_potenciometro_0 (saved by Fritzing 0.9.2b)
breadboards: 2

parts:
  Parte1 = Arduino Uno (Rev3)
  R1 = Resistor [tolerance=±5% resistance=1k package=THT]
  R2 = Rotary Potentiometer (Small) [maximum_resistance=100kΩ package=THT]
  S2 = Pushbutton [package=THT]
  R3 = Resistor [tolerance=±5% resistance=1k package=THT]
  LED1 = LED - 5mm [color="Orange (620nm)" package="5 mm [THT]"]
  LED2 = LED - 5mm [color="Red (633nm)" package="5 mm [THT]"]
  LED3 = LED - 5mm [color="Yellow (595nm)" package="5 mm [THT]"]
  LED4 = LED - 5mm [color="Blue (505nm)" package="5 mm [THT]"]
  LED5 = LED - 5mm [color="White (6500K)" package="5 mm [THT]"]
  R4 = Resistor [tolerance=±5% resistance=1k package=THT]
  R5 = Resistor [tolerance=±5% resistance=1k package=THT]
  R6 = Resistor [tolerance=±5% resistance=1k package=THT]
  R7 = Resistor [tolerance=±5% resistance=1k package=THT]

nets:
  N1: Parte1.A0, R2.wiper
  N2: Parte1.GND, R1.Pin_0, R2.leg1, LED1.cathode, LED2.cathode, LED4.cathode, LED5.cathode
  N3: Parte1.D2, R3.Pin_1
  N4: Parte1.D3_PWM, R4.Pin_1
  N5: Parte1.D4, R5.Pin_1
  N6: Parte1.D5_PWM, R6.Pin_1
  N7: Parte1.D6_PWM, R7.Pin_1
  N8: Parte1.D7, R1.Pin_1, S2.leg1
  N9: Parte1.3V3, S2.leg0
  N10: Parte1.5V, R2.leg2
  N11: R3.Pin_0, LED1.anode
  N12: LED2.anode, R4.Pin_0
  N13: LED3.anode, R5.Pin_0
  N14: LED4.anode, R6.Pin_0
  N15: LED5.anode, R7.Pin_0
