# Fritzing sketch id2392_ledmatrixdesign_0 (saved by Fritzing 0.9.3b)
breadboards: 1

parts:
  J1 = longpad pin header, 34 pins [form="long pad"]
  TOP_CHIP = IC, DIP package, 20 pins [chip_label=74HC245]
  BOTTOM_CHIP = IC, DIP package, 20 pins [chip_label=74HC245]
  J2 = longpad pin header, 7 pins [form="long pad"]  # not connected
  J3 = longpad pin header, 7 pins [form="long pad"]  # not connected
  IC3 = IC, DIP package, 20 pins [chip_label=IC]
  IC4 = IC, DIP package, 20 pins [chip_label=IC]  # not connected
  IC7 = IC, DIP package, 20 pins [chip_label=IC]  # not connected
  IC8 = IC, DIP package, 20 pins [chip_label=IC]  # not connected
  IC9 = IC, DIP package, 20 pins [chip_label=IC]  # not connected
  IC10 = IC, DIP package, 20 pins [chip_label=IC]  # not connected
  J4 = longpad pin header, 7 pins [form="long pad"]  # not connected
  J5 = longpad pin header, 7 pins [form="long pad"]  # not connected
  J6 = longpad pin header, 7 pins [form="long pad"]  # not connected
  J7 = longpad pin header, 7 pins [form="long pad"]  # not connected
  J8 = longpad pin header, 7 pins [form="long pad"]  # not connected
  J9 = longpad pin header, 7 pins [form="long pad"]  # not connected
  J10 = longpad pin header, 7 pins [form="long pad"]  # not connected
  IC12 = IC, DIP package, 8 pins [chip_label=IC]  # not connected
  IC13 = IC, DIP package, 8 pins [chip_label=IC]  # not connected
  IC11 = IC, DIP package, 16 pins [chip_label=ULN2003A]  # not connected
  C1 = Capacitor [package=axial-5mm]
  C1_2 = Capacitor [package=ctz3]
  C1_3 = Capacitor [package=ctz3]
  C1_4 = Capacitor [package=cap-pth-small2]
  C1_5 = Capacitor [package=cap-pth-small-kit]
  VCC = 4 x AAA Battery Mount

nets:
  N1: J1.pin2, J1.pin3, J1.pin4, J1.pin31, J1.pin34, C1.2, C1_2.2, C1_3.2, C1_4.2, C1_5.2, VCC.+
  N2: J1.pin7, TOP_CHIP.pin7
  N3: J1.pin9, TOP_CHIP.pin3
  N4: J1.pin10, BOTTOM_CHIP.pin8
  N5: J1.pin11, BOTTOM_CHIP.pin6
  N6: J1.pin12, BOTTOM_CHIP.pin4
  N7: J1.pin13, BOTTOM_CHIP.pin2
  GND: J1.pin14, J1.pin17, J1.pin21, TOP_CHIP.pin1, BOTTOM_CHIP.pin1
  N8: J1.pin22, BOTTOM_CHIP.pin3
  N9: J1.pin23, BOTTOM_CHIP.pin5
  N10: J1.pin26, TOP_CHIP.pin2
  N11: TOP_CHIP.pin13, IC3.pin14
  N12: TOP_CHIP.pin16, IC3.pin7
  N13: TOP_CHIP.pin19, BOTTOM_CHIP.pin19, VCC.-

notes:
  pin numbering for LED connections are
  wrong
  asterisk means
  active low
