# Fritzing sketch id2393_LEDtest_0 (saved by Fritzing 0.9.0b)
circuit board: 8.46667cm x 5.64444cm
breadboards: 1

parts:
  元件1 = Arduino Uno (Rev3)
  LED1 = LED - 5mm [color="Red (633nm)" package="5 mm [THT]"]
  R1 = Resistor [tolerance=±5% resistance=220 package=THT]
  R1_2 = Resistor [tolerance=±5% package="2512 [SMD]"]
  R1_3 = Resistor [package="0402 [SMD]"]

nets (from the breadboard view):
  N1: 元件1.D2, LED1.anode
  N2: 元件1.GND, R1.Pin_1, R1_2.Pin_1, R1_3.Pin_1
  N3: LED1.cathode, R1.Pin_0, R1_2.Pin_0, R1_3.Pin_0
