# Fritzing sketch id2394_LEDthemes_0 (saved by Fritzing 0.9.3b)
breadboards: 1

parts:
  Bauteil1 = Arduino Uno (Rev3)
  R2 = Resistor [tolerance=±5% resistance=82 package=THT]
  R5 = Resistor [tolerance=±5% resistance=150 package=THT]
  R7 = Resistor [tolerance=±5% resistance=82 package=THT]
  R9 = Resistor [tolerance=±5% resistance=82 package=THT]
  R10 = Resistor [tolerance=±5% resistance=82 package=THT]
  LED1 = LED - 5mm [color="Red (633nm)" package="5 mm [THT]"]
  LED2 = LED - 5mm [color="White (6500K)" package="5 mm [THT]"]
  LED3 = LED - 5mm [color="White (6500K)" package="5 mm [THT]"]
  LED5 = LED - 5mm [color="Green (555nm)" package="5 mm [THT]"]
  LED7 = LED - 5mm [color="White (6500K)" package="5 mm [THT]"]
  R11 = Resistor [tolerance=±5% resistance=82 package=THT]
  LED8 = LED - 5mm [color="Green (555nm)" package="5 mm [THT]"]

nets:
  N1: Bauteil1.D8, R10.Pin_0
  N2: Bauteil1.D9_PWM, R9.Pin_0
  N3: Bauteil1.D10_PWM/SS, R11.Pin_0
  N4: Bauteil1.D11_PWM/MOSI, R5.Pin_0
  N5: Bauteil1.D12/MISO, R7.Pin_0
  N6: Bauteil1.D13/SCK, R2.Pin_0
  N7: Bauteil1.GND, LED1.anode, LED2.anode, LED3.anode, LED5.anode, LED7.anode, LED8.anode
  N8: R2.Pin_1, LED2.cathode
  N9: R5.Pin_1, LED1.cathode
  N10: R7.Pin_1, LED5.cathode
  N11: R9.Pin_1, LED8.cathode
  N12: R10.Pin_1, LED7.cathode
  N13: LED3.cathode, R11.Pin_1
