# Fritzing sketch id2395_tank_0 (saved by Fritzing 0.9.3b)
breadboards: 1

parts:
  M_MOTOR1 = LEGO M MOTOR  # not connected
  XL_MOTOR1 = LEGO XL MOTOR
  Part1 = Arduino Uno (Rev3)
  XL_MOTOR2 = LEGO XL MOTOR
  Part2 = Bluetooth HC-05 Macho
  IC1 = L293D [package=THT]
  IC2 = L293D [package=THT]  # not connected
  Lego1 = lego power functions
  VCC1 = Battery block 9V

nets:
  GND: XL_MOTOR1.connector0, Part1.GND, XL_MOTOR2.connector3, Part2.GND, IC1.0V, Lego1.connector0, VCC1.-
  N1: XL_MOTOR1.connector1, IC1.Out_4_(_Controlled_by_Enable_2_)
  N2: XL_MOTOR1.connector2, IC1.Out_3_(_Controlled_by_Enable_2_)
  N3: XL_MOTOR1.connector3, XL_MOTOR2.connector0, IC1.+Vmotor, Lego1.connector3
  N4: Part1.D8, IC1.In_4
  N5: Part1.D9_PWM, IC1.Enable_1
  N6: Part1.D0/RX, Part2.TXD
  N7: Part1.D1/TX, Part2.RXD
  N8: Part1.D2, IC1.In_1
  N9: Part1.D3_PWM, IC1.Enable_2
  N10: Part1.D5_PWM, IC1.In_2
  N11: Part1.D6_PWM, IC1.In_3
  5V: Part1.5V, Part2.VCC, IC1.+V
  N12: Part1.VIN, VCC1.+
  N13: XL_MOTOR2.connector1, IC1.Out_1_(_Controlled_by_Enable_1_)
  N14: XL_MOTOR2.connector2, IC1.Out_2_(_Controlled_by_Enable_1_)
