# Fritzing sketch id2396_tank_0 (saved by Fritzing 0.9.2b)
circuit board: 8.46667cm x 5.64444cm
breadboards: 1

parts:
  Q1 = NPN-Transistor [package="TO92 [THT]"]
  Q3 = NPN-Transistor [package="TO92 [THT]"]
  IC1 = Voltage Regulator [package=to220-igo]
  IC2 = Voltage Regulator [package=to220-igo]
  R1 = Resistor [tolerance=±5% resistance=220 package=THT]
  R2 = Resistor [tolerance=±5% resistance=220 package=THT]
  R3 = Resistor [tolerance=±5% resistance=220 package=THT]
  R4 = Resistor [tolerance=±5% resistance=220 package=THT]
  DPDT = AD8561 - Ultrafast 7ns Single Supply Comparator [part_number="DPDT relay"]
  DPDT_2 = AD8561 - Ultrafast 7ns Single Supply Comparator [part_number="DPDT relay"]
  U3 = DIODE-ZENER [package=diode-zener]
  U4 = DIODE-ZENER [package=diode-zener]
  Raspberry_Pi1 = Raspberry Pi 2
  J1 = Screw terminal - 2 pins [package=THT]
  J2 = Screw terminal - 2 pins [package=THT]
  J3 = Screw terminal - 2 pins [package=THT]
  M1 = DC Motor
  M2 = DC Motor
  U5 = LIPO-2000mAh [package=lipo-2000]

nets (from the pcb view):
  N1: Q1.E, DPDT.V+, U3.A
  N2: Q1.B, Q3.B, IC1.IN, IC2.IN, Raspberry_Pi1.GND, J3.pin2, U5.-
  N3: Q1.C, R2.Pin_0
  N4: Q3.E, DPDT_2.OUTB, U4.A
  N5: Q3.C, R4.Pin_0
  N6: IC1.GND, R1.Pin_0
  N7: IC1.OUT, DPDT.V-, DPDT.GND
  N8: IC2.GND, R3.Pin_0
  N9: IC2.OUT, DPDT_2.-IN, DPDT_2.LATCH
  N10: R1.Pin_1, Raspberry_Pi1.GPIO4
  N11: R2.Pin_1, Raspberry_Pi1.GPIO17
  N12: R3.Pin_1, Raspberry_Pi1.GPIO27
  N13: R4.Pin_1, Raspberry_Pi1.GPIO22
  N14: DPDT.+IN, J1.pin2, M1.pin_2
  N15: DPDT.-IN, DPDT.LATCH, DPDT_2.V-, DPDT_2.GND, J3.pin1, U5.+
  N16: DPDT.OUT, J1.pin1, M1.pin_1
  N17: DPDT.OUTB, DPDT_2.V+, U3.C, U4.C, Raspberry_Pi1.5V
  N18: DPDT_2.+IN, J2.pin2, M2.pin_2
  N19: DPDT_2.OUT, J2.pin1, M2.pin_1
