# Fritzing sketch id2397_DESSY_FRI_0 (saved by Fritzing 0.7.5b)
breadboards: 1

parts:
  LCD1 = LCD screen
  Arduino1 = Arduino  # not connected
  RE1 = Rotary Encoder [package=THT]

nets:
  N1: LCD1.VSS, LCD1.R/W, LCD1.LED-, RE1.EncoderPinA
  N2: LCD1.VDD, LCD1.LED+, RE1.EncoderPinB
  N3: LCD1.V0, RE1.EncoderPinC
