# Fritzing sketch id2398_LevelMeter_0 (saved by Fritzing 0.7.7b)
breadboards: 1

parts:
  LED1 = LED - 5mm [color="Red (633nm)" package="5 mm [THT]"]
  LED2 = LED - 5mm [color="Red (633nm)" package="5 mm [THT]"]
  LED3 = LED - 5mm [color="Yellow (595nm)" package="5 mm [THT]"]
  LED4 = LED - 5mm [color="Yellow (595nm)" package="5 mm [THT]"]
  LED5 = LED - 5mm [color="Green (555nm)" package="5 mm [THT]"]
  LED6 = LED - 5mm [color="Green (555nm)" package="5 mm [THT]"]
  LED7 = RGB LED (com. anode, rbg) [package="5 mm [THT]"]
  R1 = Resistor [tolerance=±5% resistance=220 package=THT]
  R2 = Resistor [tolerance=±5% resistance=220 package=THT]
  R3 = Resistor [tolerance=±5% resistance=220 package=THT]
  R4 = Resistor [tolerance=±5% resistance=220 package=THT]
  R5 = Resistor [tolerance=±5% resistance=220 package=THT]
  R6 = Resistor [tolerance=±5% resistance=220 package=THT]
  R7 = Resistor [tolerance=±5% resistance=220 package=THT]
  R8 = Resistor [tolerance=±5% resistance=1.1k package=THT]
  R9 = Resistor [tolerance=±5% resistance=1.1k package=THT]
  Arduino1 = Arduino
  R11 = Rotary Potentiometer (Small) [maximum_resistance=10kΩ]
  S1 = Pushbutton [package=THT]
  R12 = Photocell (LDR) [package=THT]
  S2 = Pushbutton [package=THT]
  R13 = Resistor [tolerance=±5% resistance=10k package=THT]
  R14 = Resistor [tolerance=±5% resistance=10k package=THT]
  R15 = Resistor [tolerance=±5% resistance=10k package=THT]
  J1 = Basic Servo

nets:
  GND: LED1.cathode, LED2.cathode, LED3.cathode, LED4.cathode, LED5.cathode, LED6.cathode, Arduino1.GND, R11.leg1, R13.Pin_1, R14.Pin_1, R15.Pin_1, J1.gnd
  N1: LED1.anode, R1.Pin_1
  N2: LED2.anode, R2.Pin_1
  N3: LED3.anode, R3.Pin_1
  N4: LED4.anode, R5.Pin_1
  N5: LED5.anode, R4.Pin_1
  N6: LED6.anode, R6.Pin_1
  N7: LED7.red_cathode, R7.Pin_1
  N8: LED7.common_anode, Arduino1.3V3
  N9: LED7.blue_cathode, R8.Pin_1
  N10: LED7.green_cathode, R9.Pin_1
  N11: R1.Pin_0, Arduino1.D12
  N12: R2.Pin_0, Arduino1.D10
  N13: R3.Pin_0, Arduino1.D9
  N14: R4.Pin_0, Arduino1.D6
  N15: R5.Pin_0, Arduino1.D7
  N16: R6.Pin_0, Arduino1.D5
  N17: R7.Pin_0, R8.Pin_0, Arduino1.D2
  N18: R9.Pin_0, Arduino1.D3
  N19: Arduino1.D11, J1.pulse
  N20: Arduino1.D8, S1.leg1, R15.Pin_0
  N21: Arduino1.D4, S2.leg1, R14.Pin_0
  +5V: Arduino1.+5V, R11.leg2, S1.leg0, R12.pin_1, S2.leg0, J1.vcc
  N22: Arduino1.A3, R11.wiper
  N23: Arduino1.A5, R12.pin_0, R13.Pin_0

notes:
  Level Meter:
  LED 1 to 6
  Level Meter:
  LED 7: green,
  LED 8: red+blue
  Mode Select:
  - button A
  Level Meter Controls:
  - poti
  - photo resistor
  - button B
  Control Pointer:
  - servo
  ==== Level Meter ====
