# Fritzing sketch id2399_Levitating_Bedini_Pulse_motor_0 (saved by Fritzing 0.9.3b)
breadboards: 1

parts:
  BAT1 = DC Power [voltage=1.2]
  C8 = Electrolytic Capacitor [capacitance=100μF package="0807 [SMD, electrolytic]"]
  Q3_2N3906 = PNP-Transistor [package="TO92 [THT]"]
  Q2_2N4401 = NPN-Transistor [package="TO92 [THT]"]
  R29 = Resistor [tolerance=±5% resistance=270 package=THT]
  R27 = Resistor [tolerance=±5% resistance=100k package=THT]
  R26 = Resistor [tolerance=±5% resistance=12k package=THT]
  L1_DS10 = Inductor [package="1206 [SMD]"]
  RED_LED1 = smd LED [color="Red (660nm)" package="0603 [SMD]"]
  +_6V_SOLAR = Header 1 [package=1x01_offset]
  -_6V_SOLAR = Header 1 [package=1x01_offset]
  C9 = Tantalum Capacitor [capacitance="1 μF" package="A 3216 [SMD, tantalum]"]  # not connected
  C10 = Tantalum Capacitor [capacitance=10nF package="B 3528 [SMD, tantalum]"]  # not connected
  C11 = Ceramic Capacitor [capacitance=4.7nF package="0805 [SMD, multilayer]"]

nets:
  N1: BAT1.V+, C8.+, Q3_2N3906.E, R29.Pin_1
  N2: BAT1.V-, C8.-, Q2_2N4401.E, -_6V_SOLAR.1, C11.0
  N3: Q3_2N3906.B, R27.Pin_0, C11.1
  N4: Q3_2N3906.C, R26.Pin_0
  N5: Q2_2N4401.B, R26.Pin_1
  N6: Q2_2N4401.C, R27.Pin_1, L1_DS10.pin_1, RED_LED1.anode
  N7: R29.Pin_0, +_6V_SOLAR.1
  N8: L1_DS10.pin_0, RED_LED1.cathode

notes:
  BAT1 = 1.2V 150mah NIMH
  36awg. 4 cm ring of 300 turns
