# Fritzing sketch id239_Motion_Alarm_System_LxdKdLk_0 (saved by Fritzing 0.9.2b)
breadboards: 1

parts:
  PIR1 = PIR_sensor
  Composant1 = Arduino Uno (Rev3)
  S1 = Pushbutton [package="[THT]"]
  S2 = Pushbutton [package="[THT]"]
  S3 = Pushbutton [package="[THT]"]
  LED1 = LED - 5mm [color="Red (633nm)" package="5 mm [THT]"]
  LED2 = LED - 5mm [color="Red (633nm)" package="5 mm [THT]"]
  LED3 = LED - 5mm [color="Green (570nm)" package="5 mm [THT]"]
  J1 = Piezo Speaker
  R1 = Resistor [tolerance=±5% resistance=220 package=THT]
  R2 = Resistor [tolerance=±5% resistance=220 package=THT]
  R3 = Resistor [tolerance=±5% resistance=220 package=THT]
  R4 = Resistor [tolerance=±5% resistance=220 package=THT]
  R5 = Resistor [tolerance=±5% resistance=220 package=THT]
  R6 = Resistor [tolerance=±5% resistance=220 package=THT]

nets:
  N1: PIR1.connector1, Composant1.5V, S1.Pin_1, S1.Pin_2, S2.Pin_1, S2.Pin_2, S3.Pin_1, S3.Pin_2
  N2: PIR1.connector2, Composant1.D2
  N3: PIR1.connector3, Composant1.GND, J1.pin1, R1.Pin_0, R2.Pin_0, R3.Pin_0, R4.Pin_0, R5.Pin_0, R6.Pin_0
  N4: Composant1.D8, S3.Pin_3, S3.Pin_4, R4.Pin_1
  N5: Composant1.D9_PWM, J1.pin2
  N6: Composant1.D3_PWM, LED1.anode
  N7: Composant1.D4, LED2.anode
  N8: Composant1.D5_PWM, LED3.anode
  N9: Composant1.D6_PWM, S1.Pin_3, S1.Pin_4, R5.Pin_1
  N10: Composant1.D7, S2.Pin_3, S2.Pin_4, R6.Pin_1
  N11: LED1.cathode, R3.Pin_1
  N12: LED2.cathode, R2.Pin_1
  N13: LED3.cathode, R1.Pin_1
