# Fritzing sketch id23_Analog_Keyboard_0 (saved by Fritzing 0.9.3b)
breadboards: 1

parts:
  Part1 = Arduino Pro Mini (5V)
  Grove1 = Grove OLED 128x96
  S2 = Pushbutton [package="[THT]"]
  S3 = Pushbutton [package="[THT]"]
  R2 = Resistor [tolerance=±5% resistance=1k package="0805 [SMD]"]
  R3 = Resistor [tolerance=±5% resistance=1k package="0805 [SMD]"]
  R4 = Resistor [tolerance=±5% resistance=1k package="0805 [SMD]"]
  R5 = Resistor [tolerance=±5% resistance=1k package="0805 [SMD]"]
  R6 = Resistor [tolerance=±5% resistance=1k package="0805 [SMD]"]
  R1 = Resistor [tolerance=±5% resistance=1k package="0805 [SMD]"]
  S4 = Pushbutton [package="[THT]"]
  S5 = Pushbutton [package="[THT]"]
  S6 = Pushbutton [package="[THT]"]
  S7 = Pushbutton [package="[THT]"]
  LED1 = LEDs [package=led10mm]
  LED2 = LEDs [package=led10mm]
  R7 = Resistor [tolerance=±5% resistance=100 package="0805 [SMD]"]
  R8 = Resistor [tolerance=±5% resistance=100 package="0805 [SMD]"]

nets:
  VCC: Part1.VCC, Grove1.VCC, R1.Pin_0
  GND: Part1.GND, Grove1.GND, S2.Pin_1, S2.Pin_2, S3.Pin_1, S3.Pin_2, R6.Pin_1, S4.Pin_1, S4.Pin_2, S5.Pin_1, S5.Pin_2, S6.Pin_1, S6.Pin_2, S7.Pin_1, S7.Pin_2, S7.Pin_3
  N1: Part1.A4, Grove1.SDA
  N2: Part1.A5, Grove1.SCL
  N3: Part1.A0, S2.Pin_3, S2.Pin_4, R2.Pin_0, R1.Pin_1, R7.Pin_0, R8.Pin_0
  N4: Part1.SCK, LED1.C
  N5: Part1.MISO, LED2.C
  N6: S3.Pin_3, R2.Pin_1, R3.Pin_0
  N7: R3.Pin_1, R4.Pin_0, S4.Pin_3, S4.Pin_4
  N8: R4.Pin_1, R5.Pin_0, S5.Pin_3, S5.Pin_4
  N9: R5.Pin_1, R6.Pin_0, S6.Pin_3, S6.Pin_4
  N10: LED1.A, R7.Pin_1
  N11: LED2.A, R8.Pin_1
