# Fritzing sketch id2400_Arduino_intensiteit_0 (saved by Fritzing 0.9.2b)
breadboards: 1

parts:
  Onderdeel1 = Arduino Uno (Rev3)
  LCD1 = LCD screen
  R1 = Resistor [tolerance=±5% resistance=220 package=THT]
  R2 = Resistor [tolerance=±5% resistance=10k package=THT]
  R3 = Photocell (LDR) [package=THT]
  R4 = Rotary Potentiometer (Small) [maximum_resistance=100kΩ package=THT]  # not connected

nets:
  N1: Onderdeel1.A2, R2.Pin_1, R3.pin_1
  N2: Onderdeel1.D11_PWM/MOSI, LCD1.E
  N3: Onderdeel1.D12/MISO, LCD1.RS
  N4: Onderdeel1.D2, LCD1.DB7
  N5: Onderdeel1.D3_PWM, LCD1.DB6
  N6: Onderdeel1.D4, LCD1.DB5
  N7: Onderdeel1.D5_PWM, LCD1.DB4
  5V: Onderdeel1.5V, LCD1.VDD, R1.Pin_1, R3.pin_0
  GND: Onderdeel1.GND, LCD1.VSS, LCD1.R/W, LCD1.LED-, R2.Pin_0
  N8: LCD1.LED+, R1.Pin_0
