# Fritzing sketch id2401_wiring_0 (saved by Fritzing 0.9.3b)
circuit board: 8.46667cm x 5.64444cm
breadboards: 1

parts:
  Part1 = Arduino Uno (Rev3)
  DRV_1 = DRV8825_SID
  Motor_2 = Stepper Motor - Bipolar
  Part2 = LIDAR-Lite
  DRV_2 = DRV8825_SID
  Motor_1 = Stepper Motor - Bipolar
  C1 = Electrolytic Capacitor [capacitance=100µF package="100 mil [THT, electrolytic]"]
  R1 = Resistor [tolerance=±5% resistance=1k package=THT]
  Power_plug1 = Power plug
  C2 = Electrolytic Capacitor [capacitance=100µF package="100 mil [THT, electrolytic]"]

nets:
  N1: Part1.D8, DRV_1.connector7
  N2: Part1.D9_PWM, DRV_1.connector6
  N3: Part1.D10_PWM/SS, DRV_1.connector5
  N4: Part1.D2, R1.Pin_1
  N5: Part1.D3_PWM, Part2.connector2, R1.Pin_0
  N6: Part1.D5_PWM, DRV_2.connector7
  N7: Part1.D6_PWM, DRV_2.connector6
  N8: Part1.D7, DRV_2.connector5
  N9: Part1.5V, Part2.connector0
  N10: Part1.GND, DRV_1.connector8, Part2.connector7, DRV_2.connector8
  N11: DRV_1.connector10, Motor_2.D
  N12: DRV_1.connector11, Motor_2.B
  N13: DRV_1.connector12, Motor_2.C
  N14: DRV_1.connector13, Motor_2.A
  N15: DRV_1.connector14, DRV_2.connector14, C1.-, Power_plug1.VCC, C2.-
  N16: DRV_1.connector15, DRV_2.connector15, C1.+, Power_plug1.GND, C2.+
  N17: DRV_2.connector10, Motor_1.D
  N18: DRV_2.connector11, Motor_1.B
  N19: DRV_2.connector12, Motor_1.C
  N20: DRV_2.connector13, Motor_1.A
