# Fritzing sketch id2402_LidarLitePWM_0 (saved by Fritzing 0.9.2b)
breadboards: 1

parts:
  R1 = Resistor [tolerance=±5% resistance=1k package=THT]
  Arduino1 = Arduino Uno (Rev3)

nets:
  N1: R1.Pin_0, Arduino1.D2
  N2: R1.Pin_1, Arduino1.D3_PWM

notes:
  LIDARLite Pins
  5V MODE GND
