# Fritzing sketch id2403_Lidmotor_0 (saved by Fritzing 0.9.3b)
circuit board: 2.57593cm x 2.5263cm
breadboards: 1

parts:
  2n3906 = NPN-Transistor [part_number=2N3906 package="TO92 [THT]"]
  2n3904 = NPN-Transistor [part_number=2N3904 package="TO92 [THT]"]
  1MΩ = Resistor [tolerance=±5% resistance=1M package=THT]
  V1 = DC Power [voltage=5V]  # not connected
  LED = LED - 5mm [color="White (4500K)" package="5 mm [THT]"]
  1500Ω = Inductor [package="400 mil [THT]"]
  +_- = Battery

nets (from the pcb view):
  N1: 2n3906.E, 1MΩ.Pin_1
  N2: 2n3906.B, 1MΩ.Pin_0, LED.cathode, +_-.-
  N3: 2n3906.C, 2n3904.B
  N4: 2n3904.E, 1500Ω.pin_0, +_-.+
  N5: 2n3904.C, LED.anode, 1500Ω.pin_1
