# Fritzing sketch id2404_SCHEMA_LIFT_1_0 (saved by Fritzing 0.9.3b)

parts:
  Onderdeel1 = Arduino Uno (Rev3)
  LED1 = smd LED [color="Red (633nm)" package="0805 [SMD]"]
  U1 = ENCODER_2LED [package=encoder_led_2]
  U2 = ENCODER_2LED [package=encoder_led_2]
  IC1 = SHIFT REGISTER [package=lcc20]
  S1 = SWITCH-MOMENTARY-2 [package=tactile_switch_smd]
  U3 = 7-SEGMENT-DISPLAY [package=7-segment-display]
  R1 = Resistor [tolerance=±5% resistance=220 package=THT]  # not connected
  R2 = Resistor [tolerance=±5% resistance=220 package=THT]  # not connected
  R3 = Resistor [tolerance=±5% resistance=220 package=THT]  # not connected
  R4 = Resistor [tolerance=±5% resistance=220 package=THT]  # not connected
  R5 = Resistor [tolerance=±5% resistance=220 package=THT]  # not connected
  R6 = Resistor [tolerance=±5% resistance=220 package=THT]  # not connected
  R7 = Resistor [tolerance=±5% resistance=220 package=THT]  # not connected
  R8 = Resistor [tolerance=±5% resistance=220 package=THT]  # not connected

nets:
  N1: Onderdeel1.D8, IC1.SCK
  N2: Onderdeel1.D9_PWM, IC1.SER
  GND: Onderdeel1.GND, LED1.cathode, U1.-, U2.-, IC1.GND, IC1.G, U3.G1
  N3: Onderdeel1.D2, LED1.anode
  N4: Onderdeel1.D3_PWM, U2.SW
  N5: Onderdeel1.D4, U1.SW
  N6: Onderdeel1.D7, IC1.RCK
  5V: Onderdeel1.5V, IC1.SCL, IC1.VCC
  N7: U1.+G, S1.2
  N8: IC1.QB, U3.B
  N9: IC1.QC, U3.C
  N10: IC1.QD, U3.D
  N11: IC1.QE, U3.E
  N12: IC1.QF, U3.F
  N13: IC1.QG, U3.G
  N14: IC1.QH, U3.DP
  N15: IC1.QA, U3.A
