# Fritzing sketch id2406_SCHEMA_LIFT_2_0 (saved by Fritzing 0.9.3b)

parts:
  Onderdeel1 = Arduino Uno (Rev3)
  LED1 = smd LED [color="Red (633nm)" package="0805 [SMD]"]
  U1 = ENCODER_2LED [package=encoder_led_2]
  U2 = ENCODER_2LED [package=encoder_led_2]
  IC1 = SHIFT REGISTER [package=lcc20]
  U3 = 7-SEGMENT-DISPLAY [package=7-segment-display]
  R1 = Resistor [tolerance=±5% resistance=220 package=THT]  # not connected
  R2 = Resistor [tolerance=±5% resistance=220 package=THT]  # not connected

nets:
  N1: Onderdeel1.D8, IC1.SCK
  N2: Onderdeel1.D9_PWM, IC1.SER
  N3: Onderdeel1.D10_PWM/SS, U1.+G, U1.SW
  GND: Onderdeel1.GND, LED1.cathode, U1.-, U2.-, IC1.GND, IC1.G, U3.G1
  N4: Onderdeel1.D2, LED1.anode
  N5: Onderdeel1.D3_PWM, U2.+G, U2.SW
  N6: Onderdeel1.D7, IC1.RCK
  5V: Onderdeel1.5V, IC1.SCL, IC1.VCC
  N7: IC1.QB, U3.B
  N8: IC1.QC, U3.C
  N9: IC1.QD, U3.D
  N10: IC1.QE, U3.E
  N11: IC1.QF, U3.F
  N12: IC1.QG, U3.G
  N13: IC1.QH, U3.DP
  N14: IC1.QA, U3.A
