# Fritzing sketch id2407_SCHEMA_LIFT_2_qOSidFM_0 (saved by Fritzing 0.9.3b)

parts:
  Onderdeel1 = Arduino Uno (Rev3)
  LED1 = smd LED [color="Red (633nm)" package="0805 [SMD]"]
  IC1 = SHIFT REGISTER [package=lcc20]
  U3 = 7-SEGMENT-DISPLAY [package=7-segment-display]
  R1 = Resistor [tolerance=±5% resistance=220 package=THT]  # not connected
  R2 = Resistor [tolerance=±5% resistance=220 package=THT]
  S3 = SWITCH-MOMENTARY-2 [package=tactile-pth-12mm]
  R3 = Resistor [tolerance=±5% resistance=220 package="0603 [SMD]"]
  LED2 = LED - 5mm [color="Red (633nm)" package="5 mm [THT]"]
  S4 = SWITCH-MOMENTARY-2 [package=tactile-pth-12mm]
  R4 = Resistor [tolerance=±5% resistance=220 package="0603 [SMD]"]
  LED3 = LED - 5mm [color="Red (633nm)" package="5 mm [THT]"]
  R6 = Resistor [tolerance=±5% resistance=220 package=THT]
  R7 = Resistor [tolerance=±5% resistance=220 package=THT]

nets:
  GND: Onderdeel1.GND, LED1.cathode, IC1.GND, IC1.G, U3.G1, LED2.cathode, LED3.cathode, R7.Pin_1
  N1: Onderdeel1.D2, S4.1
  N2: Onderdeel1.D3_PWM, S3.1
  N3: Onderdeel1.D4, R2.Pin_1
  N4: Onderdeel1.D5_PWM, IC1.RCK
  N5: Onderdeel1.D6_PWM, IC1.SCK
  N6: Onderdeel1.D7, IC1.SER
  5V: Onderdeel1.5V, IC1.SCL, IC1.VCC
  N7: LED1.anode, R2.Pin_0
  N8: IC1.QB, U3.B
  N9: IC1.QC, U3.C
  N10: IC1.QD, U3.D
  N11: IC1.QE, U3.E
  N12: IC1.QF, U3.F
  N13: IC1.QG, U3.G
  N14: IC1.QH, U3.DP
  N15: IC1.QA, U3.A
  N16: S3.2, R3.Pin_0, R6.Pin_0
  N17: R3.Pin_1, LED2.anode
  N18: S4.2, R4.Pin_0, R6.Pin_1, R7.Pin_0
  N19: R4.Pin_1, LED3.anode
