# Fritzing sketch id2408_KLONER (saved by Fritzing 0.5.0b)
breadboards: 1

parts:
  Arduino1 = Arduino
  R1 = Resistor [resistance=120 package=THT]
  U1 = atmega168 [package="DIP28 [THT]"]
  R2 = Resistor [resistance=10k package=THT]
  C1 = Ceramic Capacitor [capacitance=100nF rated_voltage=35V package="100 mil [THT, multilayer]"]
  C2 = Ceramic Capacitor [capacitance=100nF rated_voltage=35V package="100 mil [THT, multilayer]"]
  XTAL1 = Crystal [package=THT]

nets:
  N1: Arduino1.connector2, U1.Pin_19
  N2: Arduino1.connector3, U1.Pin_18
  N3: Arduino1.connector4, U1.Pin_17
  N4: Arduino1.connector5, U1.Pin_1, R2.Pin_1
  N5: Arduino1.connector16, R1.Pin_0
  N6: R1.Pin_1, U1.Pin_7, U1.Pin_20, U1.Pin_21, R2.Pin_0
  N7: U1.Pin_8, U1.Pin_22, C1.1, C2.0
  N8: U1.Pin_9, C2.1, XTAL1.pin_0
  N9: U1.Pin_10, U1.Pin_11, C1.0, XTAL1.pin_1
