# Fritzing sketch id2409_KLONER_OPCIJA_DVA (saved by Fritzing 0.5.0b)
breadboards: 1

parts:
  U1 = atmega168 [package="DIP28 [THT]"]
  U2 = atmega168 [package="DIP28 [THT]"]
  S1 = Pushbutton [package="[THT]"]
  R1 = Resistor [resistance=220 package=THT]
  LED1 = green LED - 5mm [package="5 mm [THT]"]
  LED2 = yellow LED - 5mm [package="5 mm [THT]"]
  LED3 = Red LED - 5mm [package="5 mm [THT]"]
  R2 = Resistor [resistance=47 package=THT]
  R3 = Resistor [resistance=470 package=THT]
  R4 = Resistor [resistance=470 package=THT]
  XTAL1 = Crystal [package=THT]
  C1 = Ceramic Capacitor [capacitance=100nF rated_voltage=35V package="100 mil [THT, multilayer]"]
  C2 = Ceramic Capacitor [capacitance=100nF rated_voltage=35V package="100 mil [THT, multilayer]"]
  VCC1 = obsolete Battery

nets:
  N1: U1.Pin_8, U1.Pin_22, R4.Pin_1
  N2: U1.Pin_20, R2.Pin_1
  N3: U1.Pin_21, R3.Pin_1
  N4: U1.Pin_23, S1.Pin_1, S1.Pin_2, R1.Pin_0
  N5: U1.Pin_24, U2.Pin_15
  N6: U1.Pin_25, U2.Pin_3
  N7: U1.Pin_26, U2.Pin_4
  N8: U1.Pin_27, U2.Pin_5
  N9: U2.Pin_8, U2.Pin_22, U2.Pin_23, XTAL1.pin_1, C2.1
  N10: U2.Pin_24, XTAL1.pin_0, C1.0
  N11: S1.Pin_3, S1.Pin_4, VCC1.-
  N12: LED1.cathode, LED3.cathode
  N13: LED1.anode, R2.Pin_0
  N14: LED2.anode, R3.Pin_0
  N15: LED3.anode, R4.Pin_0
  N16: C1.1, C2.0

notes:
  c1 - 10pF
  c3 - 10 pF
  XTAL - 16 MHz
  RLed - 470 Ohma
  led1 - zelena
  led2 - zuta
  led 3 - crvena
  NAPAJANJE 5 VOLTI !!
