# Fritzing sketch id2410_KLONER_SA_ARDUINO_PLOCICOM (saved by Fritzing 0.5.0b)
breadboards: 1

parts:
  Arduino1 = Arduino
  U1 = atmega168 [package="DIP28 [THT]"]  # not connected
  U2 = atmega168 [package="DIP28 [THT]"]
  S1 = Pushbutton [package="[THT]"]
  LED2 = Red LED - 5mm [package="5 mm [THT]"]
  XTAL1 = Crystal [package=THT]
  C1 = Ceramic Capacitor [capacitance=100nF rated_voltage=35V package="100 mil [THT, multilayer]"]
  C2 = Ceramic Capacitor [capacitance=100nF rated_voltage=35V package="100 mil [THT, multilayer]"]
  R1 = Resistor [resistance=470 package=THT]
  R2 = Resistor [resistance=470 package=THT]
  R3 = Resistor [resistance=470 package=THT]
  R4 = Resistor [resistance=4.7k package=THT]
  LED3 = yellow LED - 5mm [package="5 mm [THT]"]
  LED1 = green LED - 5mm [package="5 mm [THT]"]

nets:
  N1: Arduino1.D13, U2.Pin_5
  N2: Arduino1.D12, U2.Pin_4
  N3: Arduino1.D11, U2.Pin_3
  N4: Arduino1.D10, U2.Pin_15
  N5: Arduino1.D9, S1.Pin_1, S1.Pin_2, R4.Pin_1
  N6: Arduino1.D8, R3.Pin_1
  N7: Arduino1.D7, R2.Pin_1
  N8: Arduino1.D6, R1.Pin_1
  N9: Arduino1.+5V, R4.Pin_0
  N10: Arduino1.GND, S1.Pin_3, S1.Pin_4
  N11: U2.Pin_6, U2.Pin_21
  N12: U2.Pin_8, U2.Pin_22, C1.0
  N13: U2.Pin_23, XTAL1.pin_1, C1.1
  N14: U2.Pin_24, XTAL1.pin_0, C2.0
  N15: LED2.cathode, LED1.cathode
  N16: LED2.anode, R1.Pin_0
  N17: R2.Pin_0, LED3.anode
  N18: R3.Pin_0, LED1.anode

notes:
  atmega 168 - cilj
  pin broj jedan je s desna na lijevo
  C1 - 10 pF
  C2 - 10 pF
  XTAL - 16 MHz
  RLEd - 1 zelena
  RLEd - 2 zuta
  RLEd - 3 crvena
