# Fritzing sketch id2410_Light_Alarm_0 (saved by Fritzing 0.8.5b)
breadboards: 1

parts:
  Part1 = Arduino Uno (Rev3)
  R1 = Resistor [tolerance=±5% resistance=220 package=THT]
  R2 = Photocell (LDR) [package=THT]
  R3 = Resistor [tolerance=±5% resistance=220 package=THT]
  LED1 = LED - 5mm [color="Red (633nm)" package="5 mm [THT]"]
  J1 = Piezo Speaker
  R4 = Resistor [tolerance=±5% resistance=220 package=THT]
  LED2 = LED - 5mm [color="Red (633nm)" package="5 mm [THT]"]
  R5 = Resistor [tolerance=±5% resistance=220 package=THT]
  LED3 = LED - 5mm [color="Red (633nm)" package="5 mm [THT]"]

nets:
  N1: Part1.D9_PWM, R3.Pin_0
  N2: Part1.D11_PWM/MOSI, J1.pin2
  N3: Part1.D13/SCK, R4.Pin_0
  N4: Part1.GND, R1.Pin_1
  N5: Part1.D3_PWM, R1.Pin_0, R2.pin_0
  N6: Part1.D7, R5.Pin_0
  N7: Part1.5V, R2.pin_1, LED1.anode, J1.pin1, LED2.anode, LED3.anode
  N8: R3.Pin_1, LED1.cathode
  N9: R4.Pin_1, LED2.cathode
  N10: R5.Pin_1, LED3.cathode

notes:
  10kΩ Resistor >
  10kΩ Resistor
  V
  Buzzer
  < Green LED
  1kΩ Resistor
  V
