# Fritzing sketch id2411_light_activated_police_siren_0 (saved by Fritzing 0.7.0b)
breadboards: 1

parts:
  U1 = 555 Timer [package="DIP8 [THT]"]
  U2 = 555 Timer [package="DIP8 [THT]"]
  R1 = Resistor [tolerance=±5% resistance=100k package=THT]
  R2 = Resistor [tolerance=±5% resistance=10k package=THT]
  R3 = Resistor [tolerance=±5% resistance=10k package=THT]
  R4 = Resistor [tolerance=±5% resistance=68k package=THT]
  C1 = Electrolytic Capacitor [capacitance=10µF voltage=16V package="100 mil [THT, electrolytic]"]
  C2 = Ceramic Capacitor [capacitance=10nF package="100 mil [THT, multilayer]"]
  D1 = Rectifier Diode [part_number=1N4148 package="300 mil [THT]"]
  R5 = Resistor [tolerance=±5% resistance=10k package=THT]
  C3 = Ceramic Capacitor [capacitance=100nF package="100 mil [THT, multilayer]"]
  Speaker = Loudspeaker
  C4 = Electrolytic Capacitor [capacitance=100µF voltage=16V package="200 mil [THT, electrolytic]"]
  VCC1 = Battery block 9V
  R6 = Trimmer Potentiometer [maximum_resistance=10kΩ package=THT]
  R7 = Resistor [tolerance=±5% resistance=100 package=THT]
  LDR = Photocell (LDR) [package=THT]
  BC547 = NPN-Transistor [package="SOT-23 [SMD]"]
  C5 = Electrolytic Capacitor [capacitance=47µF voltage=16V package="200 mil [THT, electrolytic]"]

nets:
  N1: U1.Ground, U2.Ground, C1.-, C2.1, C3.1, Speaker.pin1, VCC1.-, R6.leg2, C5.-
  N2: U1.Trigger, U1.Threshold, R4.Pin_1, D1.cathode
  N3: U1.Output, R5.Pin_0
  N4: U1.Reset, U1.Vcc_Supply_Voltage, U2.Reset, U2.Vcc_Supply_Voltage, R1.Pin_1, R3.Pin_1, BC547.1, C5.+
  N5: U1.Control_Voltage, C2.0
  N6: U1.Discharge, R1.Pin_0, R4.Pin_0, D1.anode
  N7: U2.Trigger, U2.Threshold, R2.Pin_1, C3.0
  N8: U2.Output, C4.+
  N9: U2.Control_Voltage, R5.Pin_1
  N10: U2.Discharge, R2.Pin_0, R3.Pin_0
  N11: Speaker.pin2, C4.-
  N12: VCC1.+, R7.Pin_0, LDR.pin_0
  N13: R6.wiper, LDR.pin_1, BC547.0
  N14: R7.Pin_1, BC547.2
