# Fritzing sketch id2412_LDR_0 (saved by Fritzing 0.7.5b)
breadboards: 1

parts:
  R1 = Photocell (LDR) [package=THT]
  R2 = Resistor [tolerance=±5% resistance=220 package=THT]
  Arduino1 = Arduino

nets:
  N1: R1.pin_0, Arduino1.+5V
  N2: R1.pin_1, R2.Pin_0, Arduino1.A0
  N3: R2.Pin_1, Arduino1.GND
