# Fritzing sketch id2413_LDR_0 (saved by Fritzing 0.7.1b)
breadboards: 1

parts:
  Arduino1 = Arduino
  S1 = Pushbutton [package="[THT]"]
  LED1 = LED - 5mm [color="Red (633nm)" package="5 mm [THT]"]
  R2 = Photocell (LDR) [package=THT]
  R3 = Resistor [tolerance=±5% resistance=1k package=THT]
  LED2 = LED - 5mm [color="Green (555nm)" package="5 mm [THT]"]
  R4 = Resistor [tolerance=±5% resistance=330 package=THT]
  R5 = Resistor [tolerance=±5% resistance=330 package=THT]

nets:
  N1: Arduino1.GND, S1.Pin_3, S1.Pin_4, LED1.cathode, R2.pin_0, R4.Pin_0
  N2: Arduino1.D12, LED2.anode
  N3: Arduino1.D5, R5.Pin_0
  N4: Arduino1.D2, Arduino1.+5V, S1.Pin_1, S1.Pin_2, R3.Pin_0
  N5: Arduino1.A0, R2.pin_1, R3.Pin_1
  N6: LED1.anode, R5.Pin_1
  N7: LED2.cathode, R4.Pin_1
