# Fritzing sketch id2415_KOCKA (saved by Fritzing 0.5.0b)
breadboards: 1

parts:
  Arduino1 = Arduino
  Q1 = NPN-Transistor [package="TO92 [THT]"]
  Q2 = NPN-Transistor [package="TO92 [THT]"]
  Q3 = NPN-Transistor [package="TO92 [THT]"]
  R1 = Resistor [resistance=10k package=THT]
  R2 = Resistor [resistance=10k package=THT]
  R3 = Resistor [resistance=10k package=THT]
  R4 = Resistor [resistance=220 package=THT]
  R5 = Resistor [resistance=220 package=THT]
  R6 = Resistor [resistance=220 package=THT]
  R7 = Resistor [resistance=220 package=THT]
  R8 = Resistor [resistance=220 package=THT]
  R9 = Resistor [resistance=220 package=THT]
  R10 = Resistor [resistance=220 package=THT]
  R11 = Resistor [resistance=220 package=THT]
  R12 = Resistor [resistance=220 package=THT]
  LED1 = Blue LED - 5mm [package="5 mm [THT]"]
  LED2 = Blue LED - 5mm [package="5 mm [THT]"]
  LED3 = Blue LED - 5mm [package="5 mm [THT]"]
  LED4 = Blue LED - 5mm [package="5 mm [THT]"]
  LED5 = Blue LED - 5mm [package="5 mm [THT]"]
  LED6 = Blue LED - 5mm [package="5 mm [THT]"]
  LED9 = Blue LED - 5mm [package="5 mm [THT]"]
  LED8 = Blue LED - 5mm [package="5 mm [THT]"]
  LED7 = Blue LED - 5mm [package="5 mm [THT]"]
  U1 = atmega168 [package="DIP28 [THT]"]  # not connected
  LED10 = Blue LED - 5mm [package="5 mm [THT]"]
  LED11 = Blue LED - 5mm [package="5 mm [THT]"]
  LED12 = Blue LED - 5mm [package="5 mm [THT]"]
  LED13 = Blue LED - 5mm [package="5 mm [THT]"]
  LED14 = Blue LED - 5mm [package="5 mm [THT]"]
  LED15 = Blue LED - 5mm [package="5 mm [THT]"]
  LED16 = Blue LED - 5mm [package="5 mm [THT]"]
  LED17 = Blue LED - 5mm [package="5 mm [THT]"]
  LED18 = Blue LED - 5mm [package="5 mm [THT]"]
  LED19 = Blue LED - 5mm [package="5 mm [THT]"]
  LED20 = Blue LED - 5mm [package="5 mm [THT]"]
  LED21 = Blue LED - 5mm [package="5 mm [THT]"]
  LED22 = Blue LED - 5mm [package="5 mm [THT]"]
  LED23 = Blue LED - 5mm [package="5 mm [THT]"]
  LED24 = Blue LED - 5mm [package="5 mm [THT]"]
  LED25 = Blue LED - 5mm [package="5 mm [THT]"]
  LED26 = Blue LED - 5mm [package="5 mm [THT]"]
  LED27 = Blue LED - 5mm [package="5 mm [THT]"]

nets:
  N1: Arduino1.GND, Q1.E, Q2.E, Q3.E
  N2: Arduino1.D13, Q3.B, R3.Pin_0
  N3: Arduino1.D12, Q2.B, R2.Pin_0
  N4: Arduino1.D11, Q1.B, R1.Pin_0
  N5: Arduino1.D10, R4.Pin_0
  N6: Arduino1.D9, R5.Pin_0
  N7: Arduino1.D7, R8.Pin_0
  N8: Arduino1.D6, R7.Pin_0
  N9: Arduino1.D5, R9.Pin_0
  N10: Arduino1.D4, R12.Pin_0
  N11: Arduino1.D3, R10.Pin_0
  N12: Arduino1.D2, R11.Pin_0
  N13: Arduino1.D1TX, R6.Pin_0
  N14: Q1.C, LED22.cathode, LED23.cathode, LED24.cathode, LED25.cathode, LED26.cathode, LED27.cathode
  N15: Q2.C, LED10.cathode, LED11.cathode, LED12.cathode, LED13.cathode, LED14.cathode, LED15.cathode, LED16.cathode, LED17.cathode, LED18.cathode
  N16: R4.Pin_1, LED3.anode
  N17: R5.Pin_1, LED2.anode, LED11.anode
  N18: R6.Pin_1, LED1.anode
  N19: R7.Pin_1, LED4.anode
  N20: R8.Pin_1, LED5.anode, LED23.anode
  N21: R9.Pin_1, LED6.anode
  N22: R10.Pin_1, LED9.anode, LED18.anode
  N23: R11.Pin_1, LED8.anode, LED17.anode
  N24: R12.Pin_1, LED7.anode
  N25: LED19.cathode, LED20.cathode, LED21.cathode

notes:
  Riki
