# Fritzing sketch id2415_LightDoodler_0 (saved by Fritzing 0.7.1b)
breadboards: 1

parts:
  LED = LED - 5mm [color="Red (633nm)" package="5 mm [THT]"]
  RESISTOR = Resistor [tolerance=±5% resistance=220 package=THT]
  SWITCH = Pushbutton [package="[THT]"]
  +_BAT_- = Battery

nets:
  N1: LED.cathode, SWITCH.Pin_3, SWITCH.Pin_4
  N2: LED.anode, RESISTOR.Pin_0
  N3: RESISTOR.Pin_1, +_BAT_-.+
  N4: SWITCH.Pin_1, SWITCH.Pin_2, +_BAT_-.-

notes:
  LIGHTDOODLER V1
