# Fritzing sketch id2416_light_level_sensor_0 (saved by Fritzing 0.9.0b)
circuit board: 8.84055cm x 6.40467cm
breadboards: 1

parts:
  Part1 = Arduino Uno (Rev3)
  R1 = Resistor [tolerance=±5% resistance=10k package=THT]
  LED1 = LED - 5mm [color="Green (555nm)" package="5 mm [THT]"]
  IC1 = IC, DIP package, 16 pins [chip_label="IC 7447"]
  7_Segment1 = 7 Segment Display
  LED2 = LED - 5mm [color="Yellow (585nm)" package="5 mm [THT]"]
  LED3 = LED - 5mm [color="Yellow (585nm)" package="5 mm [THT]"]
  LED4 = LED - 5mm [color="Red (633nm)" package="5 mm [THT]"]
  LED5 = LED - 5mm [color="Red (633nm)" package="5 mm [THT]"]
  R2 = Resistor [tolerance=±5% resistance=10k package=THT]
  R3 = Resistor [tolerance=±5% resistance=10k package=THT]
  R4 = Resistor [tolerance=±5% resistance=10k package=THT]
  R5 = Resistor [tolerance=±5% resistance=10k package=THT]
  R6 = Resistor [tolerance=±5% resistance=10k package=THT]
  R7 = Resistor [tolerance=±5% resistance=10k package=THT]
  IR1 = LED - 5mm [color="Infrared (940nm)" package="5 mm [THT]"]
  IR2 = LED - 5mm [color="Infrared (940nm)" package="5 mm [THT]"]

nets:
  N1: Part1.A5/SCL, R7.Pin_0, IR1.cathode, IR2.cathode
  N2: Part1.D8, LED3.anode
  N3: Part1.D9_PWM, LED4.anode
  N4: Part1.D10_PWM/SS, LED5.anode
  N5: Part1.D2, IC1.pin7
  N6: Part1.D3_PWM, IC1.pin1
  N7: Part1.D4, IC1.pin2
  N8: Part1.D5_PWM, IC1.pin6
  N9: Part1.D6_PWM, LED1.anode
  N10: Part1.D7, LED2.anode
  N11: R1.Pin_0, LED1.cathode
  N12: R1.Pin_1, IC1.pin8, R2.Pin_1, R3.Pin_1, R4.Pin_1, R5.Pin_1, IR1.anode, IR2.anode
  N13: IC1.pin9, 7_Segment1.Segment_E
  N14: IC1.pin10, 7_Segment1.Segment_D
  N15: IC1.pin11, 7_Segment1.Segment_DP
  N16: IC1.pin12, 7_Segment1.Segment_B
  N17: IC1.pin13, 7_Segment1.Segment_A
  N18: IC1.pin14, 7_Segment1.Segment_G
  N19: IC1.pin15, 7_Segment1.Segment_F
  N20: IC1.pin16, R6.Pin_0, R7.Pin_1
  N21: 7_Segment1.common_anode, R6.Pin_1
  N22: LED2.cathode, R2.Pin_0
  N23: LED3.cathode, R3.Pin_0
  N24: LED4.cathode, R4.Pin_0
  N25: LED5.cathode, R5.Pin_0

notes:
  -
  VCC = 5V
  +
