# Fritzing sketch id2417_LightMeter_0 (saved by Fritzing 0.9.0b)
circuit board: 9.07572cm x 6.28933cm
breadboards: 1

parts:
  Eleman1 = Arduino Uno (Rev3)
  R1 = Photocell (LDR) [package=THT]
  LED4 = LED - 5mm [color="Red (633nm)" package="5 mm [THT]"]
  LED5 = LED - 5mm [color="Red (633nm)" package="5 mm [THT]"]
  LED6 = LED - 5mm [color="Red (633nm)" package="5 mm [THT]"]
  R2 = Resistor [tolerance=±5% resistance=220k package=THT]
  R3 = Resistor [tolerance=±5% resistance=220k package=THT]
  R4 = Resistor [tolerance=±5% resistance=220k package=THT]
  R5 = Resistor [tolerance=±5% resistance=680 package=THT]

nets:
  N1: Eleman1.A0, R1.pin_0, R5.Pin_0
  N2: Eleman1.GND, LED4.cathode, LED5.cathode, LED6.anode, R5.Pin_1
  N3: Eleman1.D4, R4.Pin_1
  N4: Eleman1.D5_PWM, R3.Pin_1
  N5: Eleman1.D6_PWM, R2.Pin_1
  N6: Eleman1.5V, R1.pin_1
  N7: LED4.anode, R2.Pin_0
  N8: LED5.anode, R3.Pin_0
  N9: LED6.cathode, R4.Pin_0
