# Fritzing sketch id2418_Memo_sketch_0 (saved by Fritzing 0.9.0b)
breadboards: 1

parts:
  R1 = Resistor [tolerance=±5% resistance=10k package=THT]
  R2 = PHOTOCELL [package=photocell-kit]
  R3 = Resistor [tolerance=±5% resistance=330 package=THT]
  LED1 = LED - 5mm [color="Red (633nm)" package="5 mm [THT]"]
  J1 = Basic Servo
  Part5 = Arduino Leonardo (Rev3b)

nets:
  GND: R1.Pin_0, R3.Pin_0, J1.gnd, Part5.GND
  N1: R1.Pin_1, R2.P$2, Part5.A1
  VCC: R2.P$1, J1.vcc, Part5.5V
  N2: R3.Pin_1, LED1.anode
  N3: LED1.cathode, Part5.D5_PWM
  N4: J1.pulse, Part5.D9_PWM/A9

notes:
  RedBoard
