# Fritzing sketch id2419_screamer_v22_0 (saved by Fritzing 0.9.1b)
circuit board: 5cm x 4cm
breadboards: 1

parts:
  SPK = Piezo Speaker [part_number=SPK]
  C2_10uF = Electrolytic Capacitor [capacitance=10µF package="100 mil [THT, electrolytic]"]
  LDR = Photocell (LDR) [package=THT]
  R2 = Resistor [tolerance=±5% resistance=1k package=THT]
  555 = IC, DIP package, 8 pins [chip_label=IC]
  C1_100nF = nis_c_200
  Pad1 = Pad [width=5.31359533333333 height=3.98613054700854 connect=center]  # not connected
  Pad2 = Pad [width=5.18331938461538 height=3.87760524786325 connect=center]  # not connected
  VCC1 = Battery block 9V

nets:
  N1: SPK.pin1, C2_10uF.-
  N2: C2_10uF.+, LDR.pin_0, 555.pin3
  N3: LDR.pin_1, R2.Pin_0
  N4: R2.Pin_1, 555.pin2, 555.pin6, C1_100nF.connector1
  N5: 555.pin1, C1_100nF.connector0, VCC1.-
  N6: 555.pin4, 555.pin8

notes:
  Schrotty
  Screamer
  -
  +
  SPK
  nis
