# Fritzing sketch id2420_lightSensingLED_0 (saved by Fritzing 0.9.2b)
breadboards: 1

parts:
  R1 = Resistor [tolerance=±5% resistance=300 package=THT]
  LED1 = LED - 5mm [color="Red (633nm)" package="5 mm [THT]"]
  Part1 = Arduino Uno (Rev3)
  R2 = Photocell (LDR) [package=THT]
  R3 = Resistor [tolerance=±5% resistance=300 package=THT]

nets:
  N1: R1.Pin_0, Part1.GND, R3.Pin_1
  N2: R1.Pin_1, LED1.cathode
  N3: LED1.anode, Part1.D10_PWM/SS
  N4: Part1.A0, R2.pin_1, R3.Pin_0
  N5: Part1.5V, R2.pin_0
