# Fritzing sketch id2421_schematic_for_light_sensitive_light_and_servo_0 (saved by Fritzing 0.8.5b)
circuit board: 8.46667cm x 5.64444cm
breadboards: 1

parts:
  Part1 = Arduino Uno (Rev3)
  LED1 = LED - 5mm [color="Red (633nm)" package="5 mm [THT]"]
  R1 = Resistor [tolerance=±5% resistance=220 package=THT]
  R2 = Resistor [tolerance=±5% resistance=10k package=THT]
  R3 = Photocell (LDR) [package=THT]
  J1 = Basic Servo

nets:
  N1: Part1.A0, R2.Pin_1, R3.pin_0
  N2: Part1.D9_PWM, J1.pulse
  N3: Part1.D13/SCK, R1.Pin_0
  GND: Part1.GND, LED1.cathode, R3.pin_1, J1.gnd
  N4: Part1.3V3, R2.Pin_0
  5V: Part1.5V, J1.vcc
  N5: LED1.anode, R1.Pin_1
