# Fritzing sketch id2422_light_sensor_0 (saved by Fritzing 0.3.19b)
breadboards: 1

parts:
  Arduino1 = Arduino
  R1 = Photocell (LDR) [package=THT]
  R2 = Resistor [resistance=220 package=THT]
  LED3 = Red LED - 5mm
  LED1 = yellow LED - 5mm
  LED2 = white LED - 5mm

nets:
  N1: Arduino1.GND, R2.Pin_1, LED3.cathode, LED1.cathode, LED2.cathode
  N2: Arduino1.D11, LED1.anode
  N3: Arduino1.D10, LED2.anode
  N4: Arduino1.D9, LED3.anode
  N5: Arduino1.+5V, R1.pin_0
  N6: Arduino1.A0, R1.pin_1, R2.Pin_0
