# Fritzing sketch id2423_Light_Sensor_Logger_0 (saved by Fritzing 0.9.3b)
circuit board: 8.46667cm x 5.64444cm
breadboards: 1

parts:
  WeMos_D1_Mini1 = WeMos D1 Mini
  R1 = Resistor [tolerance=±5% resistance=2.2k package="1206 [SMD]"]
  R2 = Photocell (LDR) [package=THT]

nets:
  N1: WeMos_D1_Mini1.3V3, R2.pin_1
  N2: WeMos_D1_Mini1.A0, R1.Pin_0, R2.pin_0
  N3: WeMos_D1_Mini1.G, R1.Pin_1
