# Fritzing sketch id2424_first_light_indicator_0 (saved by Fritzing 0.9.2b)
circuit board: 8.46667cm x 5.64444cm
breadboards: 1

parts:
  Part1 = Arduino Uno (Rev3) - ICSP
  R1 = Photocell (LDR) [package=THT]
  R2 = Resistor [tolerance=±5% resistance=10k package=THT]
  LED1 = LED - 5mm [color="Red (633nm)" package="5 mm [THT]"]
  LED2 = LED - 5mm [color="Red (633nm)" package="5 mm [THT]"]
  LED3 = LED - 5mm [color="Yellow (595nm)" package="5 mm [THT]"]
  LED4 = LED - 5mm [color="Yellow (595nm)" package="5 mm [THT]"]
  LED5 = LED - 5mm [color="Green (560nm)" package="5 mm [THT]"]
  LED6 = LED - 5mm [color="Green (560nm)" package="5 mm [THT]"]
  R3 = Resistor [tolerance=±5% resistance=10k package=THT]
  R4 = Resistor [tolerance=±5% resistance=10k package=THT]
  R5 = Resistor [tolerance=±5% resistance=10k package=THT]
  R6 = Resistor [tolerance=±5% resistance=10k package=THT]
  R7 = Resistor [tolerance=±5% resistance=10k package=THT]
  R8 = Resistor [tolerance=±5% resistance=10k package=THT]

nets:
  N1: Part1.A0, R1.pin_1, R2.Pin_0
  N2: Part1.ICSP_MOSI, Part1.D11_PWM/MOSI, LED1.anode
  N3: Part1.5V, R1.pin_0
  N4: Part1.D9_PWM, LED3.anode
  N5: Part1.D10_PWM/SS, LED2.anode
  N6: Part1.GND, R2.Pin_1, R3.Pin_1, R4.Pin_1, R5.Pin_1, R6.Pin_1, R7.Pin_1, R8.Pin_1
  N7: Part1.D3_PWM, LED6.anode
  N8: Part1.D5_PWM, LED5.anode
  N9: Part1.D6_PWM, LED4.anode
  N10: LED1.cathode, R3.Pin_0
  N11: LED2.cathode, R4.Pin_0
  N12: LED3.cathode, R5.Pin_0
  N13: LED4.cathode, R6.Pin_0
  N14: LED5.cathode, R7.Pin_0
  N15: LED6.cathode, R8.Pin_0
