# Fritzing sketch id2425_fotocelda_inversor_0 (saved by Fritzing 0.8.3b)
breadboards: 1

parts:
  R1 = Photocell (LDR) [package=THT]
  Q1 = NPN-Transistor [package="TO92 [THT]"]
  D1 = Rectifier Diode [part_number=1N4001 package="300 mil [THT]"]
  U1 = Voltage Regulator - 5V [package="TO220 [THT]"]
  IC1 = Hex Inverter Schmitt Trigger SN74HC14 [package="DIP (Dual Inline)"]
  BAT1 = BC9VPC [package=bc9vpc]
  R2 = Rotary Potentiometer (Large) [package=THT]
  LED1 = LED - 3mm [color="Red (633nm)" package="3 mm [THT]"]
  U2 = RELAY-2 [package=relay-g5v]
  R3 = Resistor [tolerance=±5% resistance=1k package=THT]

nets:
  N1: R1.pin_0, IC1.1A, R2.leg1
  N2: R1.pin_1, D1.cathode, U1.output_voltage, IC1.VCC, BAT1.V-, U2.9
  GND: Q1.E, U1.GND, IC1.GND, BAT1.V+, R2.wiper, LED1.anode
  N3: Q1.B, R3.Pin_1
  N4: Q1.C, D1.anode, U2.2
  N5: IC1.1Y, LED1.cathode, R3.Pin_0
