# Fritzing sketch id2426_cds_led_fritzing_0 (saved by Fritzing 0.9.3b)
breadboards: 1

parts:
  R1 = PHOTOCELL [package=photocell]
  LED1 = smd LED [color="Red (633nm)" package="1206 [SMD]"]
  R2 = Resistor [tolerance=±5% resistance=220 package=THT]
  R3 = Resistor [tolerance=±5% resistance=10k package=THT]
  부품1 = Arduino Uno (Rev3)

nets:
  N1: R1.P$1, LED1.cathode, 부품1.GND
  N2: R1.P$2, R3.Pin_0
  N3: LED1.anode, R2.Pin_0
  N4: R2.Pin_1, 부품1.D9_PWM
  N5: R3.Pin_1, 부품1.5V
