# Fritzing sketch id2427_lightsensor_0 (saved by Fritzing 0.9.2b)
breadboards: 1

parts:
  Part1 = Arduino Uno (Rev3) - ICSP
  R1 = PHOTOCELL [package=photocell-kit]
  R2 = Resistor [tolerance=±5% resistance=220 package=THT]
  LED1 = LED - 5mm [color="Red (633nm)" package="5 mm [THT]"]
  R3 = Resistor [tolerance=±5% resistance=220 package=THT]

nets:
  N1: Part1.A0, R1.P$2, R2.Pin_0
  N2: Part1.D13/SCK, R3.Pin_1
  N3: Part1.GND, R2.Pin_1, LED1.cathode
  N4: Part1.5V, R1.P$1
  N5: LED1.anode, R3.Pin_0
