# Fritzing sketch id2429_Lightcontrol_0 (saved by Fritzing 0.9.3b)
breadboards: 1

parts:
  Part1 = Arduino Micro (Rev3)
  R1 = Rotary Potentiometer (Small) [maximum_resistance=100kΩ package=THT]  # not connected
  R2 = Rotary Potentiometer (Small) [maximum_resistance=100kΩ package=THT]
  R3 = Rotary Potentiometer (Small) [maximum_resistance=100kΩ package=THT]
  R5 = Resistor [tolerance=±5% resistance=10k package="1206 [SMD]"]
  S1 = Toggle Switch [package=THT]
  R6 = Rotary Potentiometer (Small) [maximum_resistance=100kΩ package=THT]
  LED1 = RGB LED (com. cathode, rgb) [package="5 mm [THT]"]

nets:
  N1: Part1.GND, R2.wiper, R3.wiper, R5.Pin_0, R6.wiper, LED1.blue_anode
  N2: Part1.D2/SDA, R5.Pin_1, S1.COM
  N3: Part1.5V, R2.leg1, R3.leg1, S1.L2, R6.leg1
  N4: Part1.A3, R6.leg2
  N5: Part1.A2, R3.leg2
  N6: Part1.A1, R2.leg2
