# Fritzing sketch id242_2016_02_03_0 (saved by Fritzing 0.9.2b)
breadboards: 2

parts:
  Part1 = Arduino Uno (Rev3)
  Q1 = PHOTOTRANSISTOR REFLECTIVE OBJECT SENSOR [package=qrb1114-side]
  U1 = LCD-16X2 [package=lcd-16x2_noholes]
  U2 = POT [package=pot_mammoth]
  S1 = Round Pushbutton
  R1 = Resistor [tolerance=±5% resistance=15k package="2010 [SMD]"]
  R2 = Resistor [tolerance=±5% resistance=180k package="2010 [SMD]"]
  C2 = Tantalum Capacitor [capacitance="1 μF" package="B 3528 [SMD, tantalum]"]
  C3 = Tantalum Capacitor [capacitance="1 μF" package="B 3528 [SMD, tantalum]"]
  C4 = Electrolytic Capacitor [capacitance=100µF package="200 mil [THT, electrolytic]"]

nets:
  N1: Part1.D8, U1.E
  N2: Part1.D2, Q1.E, R1.Pin_0
  N3: Part1.D3_PWM, U1.DB6
  N4: Part1.D4, U1.DB5
  N5: Part1.D5_PWM, U1.DB4
  N6: Part1.D6_PWM, U1.DB7
  N7: Part1.D7, U1.RS
  5V: Part1.5V, U1.VDD, U1.A, U2.E, S1.leg0, R1.Pin_1, R2.Pin_1, C2.-, C3.-, C4.-
  GND: Part1.GND, Q1.C, Q1.K, U1.VSS, U1.R_W, U1.K, U2.S, S1.leg1, C2.+, C3.+, C4.+
  N8: Q1.A, R2.Pin_0
  N9: U1.VO, U2.A

notes:
  Se heliosoph.mit-links.info/photointerrupter-basics/
