# Fritzing sketch id2430_FritzingSketch12_Sep_16_0 (saved by Fritzing 0.9.3b)
breadboards: 4

parts:
  Part1 = Arduino Nano (Rev3.0)  # not connected
  R2 = Resistor [tolerance=±5% resistance=330 package=THT]
  R4 = Resistor [tolerance=±5% resistance=330 package=THT]
  R5 = Resistor [tolerance=±5% resistance=330 package=THT]
  R6 = Resistor [tolerance=±5% resistance=330 package=THT]
  R7 = Resistor [tolerance=±5% resistance=330 package=THT]
  R8 = Resistor [tolerance=±5% resistance=330 package=THT]
  R9 = Resistor [tolerance=±5% resistance=330 package=THT]
  R10 = Resistor [tolerance=±5% resistance=330 package=THT]
  R11 = Resistor [tolerance=±5% resistance=330 package=THT]
  R12 = Resistor [tolerance=±5% resistance=330 package=THT]
  R13 = Resistor [tolerance=±5% resistance=330 package=THT]
  R14 = Resistor [tolerance=±5% resistance=330 package=THT]
  R15 = Resistor [tolerance=±5% resistance=330 package=THT]
  R16 = Resistor [tolerance=±5% resistance=330 package=THT]
  U2 = 74HC595 [package="DIP16 [THT]"]
  U3 = 74HC595 [package="DIP16 [THT]"]
  U4 = 74HC595 [package="DIP16 [THT]"]
  U5 = 74HC595 [package="DIP16 [THT]"]
  R36 = Resistor [tolerance=±5% resistance=330 package=THT]
  R37 = Resistor [tolerance=±5% resistance=330 package=THT]
  LED1 = LED - 5mm [color="Red (633nm)" package="5 mm [THT]"]
  R38 = Resistor [tolerance=±5% resistance=330 package=THT]
  R39 = Resistor [tolerance=±5% resistance=330 package=THT]
  R40 = Resistor [tolerance=±5% resistance=330 package=THT]
  R41 = Resistor [tolerance=±5% resistance=330 package=THT]
  R42 = Resistor [tolerance=±5% resistance=330 package=THT]
  R43 = Resistor [tolerance=±5% resistance=330 package=THT]
  R44 = Resistor [tolerance=±5% resistance=330 package=THT]
  R45 = Resistor [tolerance=±5% resistance=330 package=THT]
  R46 = Resistor [tolerance=±5% resistance=330 package=THT]
  R47 = Resistor [tolerance=±5% resistance=330 package=THT]
  R48 = Resistor [tolerance=±5% resistance=330 package=THT]
  R49 = Resistor [tolerance=±5% resistance=330 package=THT]
  R50 = Resistor [tolerance=±5% resistance=330 package=THT]
  R51 = Resistor [tolerance=±5% resistance=330 package=THT]
  R52 = Resistor [tolerance=±5% resistance=330 package=THT]
  R53 = Resistor [tolerance=±5% resistance=330 package=THT]  # not connected
  LED2 = LED - 5mm [color="Red (633nm)" package="5 mm [THT]"]
  LED3 = LED - 5mm [color="Red (633nm)" package="5 mm [THT]"]
  LED4 = LED - 5mm [color="Red (633nm)" package="5 mm [THT]"]
  LED5 = LED - 5mm [color="Red (633nm)" package="5 mm [THT]"]
  LED6 = LED - 5mm [color="Red (633nm)" package="5 mm [THT]"]
  LED7 = LED - 5mm [color="Red (633nm)" package="5 mm [THT]"]
  LED8 = LED - 5mm [color="Red (633nm)" package="5 mm [THT]"]
  LED9 = LED - 5mm [color="Red (633nm)" package="5 mm [THT]"]
  LED10 = LED - 5mm [color="Red (633nm)" package="5 mm [THT]"]
  LED11 = LED - 5mm [color="Red (633nm)" package="5 mm [THT]"]
  LED12 = LED - 5mm [color="Red (633nm)" package="5 mm [THT]"]
  LED13 = LED - 5mm [color="Red (633nm)" package="5 mm [THT]"]
  LED14 = LED - 5mm [color="Red (633nm)" package="5 mm [THT]"]
  LED15 = LED - 5mm [color="Red (633nm)" package="5 mm [THT]"]
  LED16 = LED - 5mm [color="Red (633nm)" package="5 mm [THT]"]
  LED17 = LED - 5mm [color="Red (633nm)" package="5 mm [THT]"]
  LED18 = LED - 5mm [color="Red (633nm)" package="5 mm [THT]"]
  LED19 = LED - 5mm [color="Red (633nm)" package="5 mm [THT]"]
  LED20 = LED - 5mm [color="Red (633nm)" package="5 mm [THT]"]
  LED21 = LED - 5mm [color="Red (633nm)" package="5 mm [THT]"]
  LED22 = LED - 5mm [color="Red (633nm)" package="5 mm [THT]"]
  LED23 = LED - 5mm [color="Red (633nm)" package="5 mm [THT]"]
  LED24 = LED - 5mm [color="Red (633nm)" package="5 mm [THT]"]
  LED25 = LED - 5mm [color="Red (633nm)" package="5 mm [THT]"]
  LED26 = LED - 5mm [color="Red (633nm)" package="5 mm [THT]"]
  LED27 = LED - 5mm [color="Red (633nm)" package="5 mm [THT]"]
  LED28 = LED - 5mm [color="Red (633nm)" package="5 mm [THT]"]
  LED29 = LED - 5mm [color="Red (633nm)" package="5 mm [THT]"]
  LED30 = LED - 5mm [color="Red (633nm)" package="5 mm [THT]"]
  LED31 = LED - 5mm [color="Red (633nm)" package="5 mm [THT]"]
  LED32 = LED - 5mm [color="Red (633nm)" package="5 mm [THT]"]

nets:
  N1: R2.Pin_0, R48.Pin_0, LED13.anode, LED17.anode, LED25.cathode, LED29.cathode
  N2: R4.Pin_0, R8.Pin_0, R9.Pin_0, R12.Pin_0, R13.Pin_0, R14.Pin_0, R16.Pin_0, U5.OE, LED1.anode, R39.Pin_0, R40.Pin_0, R44.Pin_0, LED4.anode, LED5.cathode, LED5.anode, LED8.cathode, LED9.cathode, LED9.anode, LED10.cathode, LED10.anode, LED12.anode, LED16.anode, LED19.anode, LED31.anode, LED32.cathode, LED32.anode
  N3: R4.Pin_1, U5.Q1
  N4: R5.Pin_0, R6.Pin_0
  N5: R5.Pin_1, U5.Q2
  N6: R6.Pin_1, U5.Q3
  N7: R7.Pin_0, R11.Pin_0
  N8: R7.Pin_1, U5.Q7
  N9: R8.Pin_1, U5.Q6
  N10: R9.Pin_1, U5.Q5
  N11: R10.Pin_1, U5.Q4
  N12: R12.Pin_1, U2.Q3
  N13: R13.Pin_1, U2.Q2
  N14: R14.Pin_1, U2.Q1
  N15: R15.Pin_0, R51.Pin_0, LED3.cathode, LED3.anode, LED4.cathode, LED20.anode, LED27.cathode, LED31.cathode
  N16: R15.Pin_1, U2.Q5
  N17: R16.Pin_1, U2.Q4
  N18: U2.Q6, R36.Pin_1
  N19: U2.Q7, R37.Pin_1
  GND: U2.GND, U5.GND
  N20: U2.SH_CP, U3.SH_CP, U4.SH_CP, U5.SH_CP
  VCC: U2.VCC, U3.MR, U3.VCC, U4.VCC
  N21: U3.Q1, R42.Pin_1
  N22: U3.Q2, R43.Pin_1
  N23: U3.Q3, R44.Pin_1
  N24: U3.Q4, R39.Pin_1
  N25: U3.Q5, R41.Pin_1
  N26: U3.Q6, R38.Pin_1
  N27: U3.Q7, R40.Pin_1
  GND_2: U3.GND, U4.GND, U4.OE
  N28: U3.ST_CP, U4.ST_CP
  N29: U3.DS, U4.Q7'
  N30: U4.Q1, R52.Pin_1
  N31: U4.Q2, R51.Pin_1
  N32: U4.Q3, R50.Pin_1
  N33: U4.Q4, R46.Pin_1
  N34: U4.Q5, R47.Pin_1
  N35: U4.Q6, R48.Pin_1
  N36: U4.Q7, R49.Pin_1
  N37: LED1.cathode, LED15.anode
  N38: R38.Pin_0, R41.Pin_0
  N39: R42.Pin_0, R43.Pin_0
  N40: R45.Pin_0, R49.Pin_0
  N41: R46.Pin_0, R52.Pin_0
  N42: LED2.anode, LED6.cathode, LED14.anode, LED18.anode, LED26.cathode
  N43: LED7.anode, LED8.anode
  N44: LED11.cathode, LED14.cathode
  N45: LED13.cathode, LED16.cathode
  N46: LED17.cathode, LED19.cathode, LED20.cathode, LED21.cathode
  N47: LED22.cathode, LED24.cathode
  N48: LED22.anode, LED23.anode
  N49: LED24.anode, LED25.anode, LED27.anode
  N50: LED28.cathode, LED30.cathode
  N51: LED28.anode, LED29.anode, LED30.anode
