# Fritzing sketch id2431_trafficLight_0 (saved by Fritzing 0.9.2b)
breadboards: 1

parts:
  Часть1 = Arduino Uno (Rev3)
  S1 = Pushbutton [package="[THT]"]
  R1 = Resistor [tolerance=±5% resistance=220 package=THT]
  LED1 = LED - 5mm [color="Red (633nm)" package="5 mm [THT]"]
  LED2 = LED - 5mm [color="Yellow (585nm)" package="5 mm [THT]"]
  LED3 = LED - 5mm [color="Green (555nm)" package="5 mm [THT]"]
  R2 = Resistor [tolerance=±5% resistance=220 package=THT]
  R3 = Resistor [tolerance=±5% resistance=220 package=THT]
  R4 = Resistor [tolerance=±5% resistance=220 package=THT]
  LED4 = LED - 5mm [color="Red (633nm)" package="5 mm [THT]"]
  LED5 = LED - 5mm [color="Green (555nm)" package="5 mm [THT]"]
  R5 = Resistor [tolerance=±5% resistance=220 package=THT]
  R6 = Resistor [tolerance=±5% resistance=220 package=THT]

nets:
  N1: Часть1.D9_PWM, R5.Pin_0
  N2: Часть1.D10_PWM/SS, R6.Pin_0
  N3: Часть1.D11_PWM/MOSI, R2.Pin_0
  N4: Часть1.D12/MISO, R3.Pin_0
  N5: Часть1.D13/SCK, R4.Pin_0
  N6: Часть1.D5_PWM, S1.Pin_3, S1.Pin_4, R1.Pin_1
  N7: Часть1.5V, S1.Pin_1, S1.Pin_2
  N8: Часть1.GND, R1.Pin_0, LED1.cathode, LED2.cathode, LED3.cathode
  N9: LED1.anode, R2.Pin_1
  N10: LED2.anode, R3.Pin_1
  N11: LED3.anode, R4.Pin_1
  N12: LED4.anode, R5.Pin_1
  N13: LED5.anode, R6.Pin_1
