# Fritzing sketch id2432_lightSensor_0 (saved by Fritzing 0.9.3b)
circuit board: 10.52cm x 9.20434cm
breadboards: 1

parts:
  Часть1 = Arduino Uno (Rev3)
  R1 = Resistor [tolerance=±5% resistance=220 package=THT]
  R2 = Resistor [tolerance=±5% resistance=220 package=THT]
  R3 = Resistor [tolerance=±5% resistance=220 package=THT]
  LED1 = RGB LED (com. cathode, rgb) [package="5 mm [THT]"]
  R4 = Photocell (LDR) [package=THT]
  R5 = Resistor [tolerance=±5% resistance=1k package=THT]

nets:
  N1: Часть1.A1, R4.pin_1, R5.Pin_0
  N2: Часть1.D9_PWM, R3.Pin_0
  N3: Часть1.D10_PWM/SS, R2.Pin_0
  N4: Часть1.D11_PWM/MOSI, R1.Pin_0
  N5: Часть1.5V, R4.pin_0
  N6: Часть1.GND, LED1.common_cathode, R5.Pin_1
  N7: R1.Pin_1, LED1.blue_anode
  N8: R2.Pin_1, LED1.green_anode
  N9: R3.Pin_1, LED1.red_anode
