# Fritzing sketch id2435_Floorboard_Arduino_0 (saved by Fritzing 0.9.2b)
breadboards: 1

parts:
  1 = Arduino Nano (Rev3.0) (ICSP)
  R2 = Resistor [tolerance=±5% resistance=10k package="2010 [SMD]"]
  R1 = Resistor [tolerance=±5% resistance=1k package="2010 [SMD]"]
  R3 = Resistor [tolerance=±5% resistance=10k package="2010 [SMD]"]
  U1 = RJ45 Jack [package=rj45-8]

nets:
  GND: 1.GND, U1.1, U1.3
  N1: 1.D8, U1.5
  N2: 1.5V, R2.Pin_1, R1.Pin_1, R3.Pin_1, U1.7, U1.8
  N3: 1.A5, R3.Pin_0, U1.4
  N4: 1.A4, R2.Pin_0, U1.2
  N5: 1.A3, R1.Pin_0, U1.6

notes:
  Pullup
