# Fritzing sketch id2436_LFR_Circuit_0 (saved by Fritzing 0.9.0b)
breadboards: 4

parts:
  C1 = Tantalum Capacitor [capacitance=100nF voltage=50V package="100 mil [THT, tantalum]"]
  Q1 = NPN-Transistor [part_number=P2N2222A package="TO92 [THT]"]
  R1 = Resistor [tolerance=±5% resistance=100 package=THT]
  M1 = DC Motor
  C2 = Tantalum Capacitor [capacitance=100nF voltage=50V package="100 mil [THT, tantalum]"]
  Q2 = NPN-Transistor [part_number=P2N2222A package="TO92 [THT]"]
  R2 = Resistor [tolerance=±5% resistance=100 package=THT]
  M2 = DC Motor
  Part1 = Arduino Uno (Rev3)
  R3 = Resistor [tolerance=±5% resistance=220 package=THT]
  R4 = Photocell (LDR) [package=THT]
  LED1 = LED - 5mm [color="Blue (470nm)" package="5 mm [THT]"]
  R5 = Resistor [tolerance=±5% resistance=2.2k package=THT]
  R6 = Resistor [tolerance=±5% resistance=2.2k package=THT]
  LED2 = LED - 5mm [color="Blue (470nm)" package="5 mm [THT]"]
  R7 = Resistor [tolerance=±5% resistance=220 package=THT]
  R8 = Photocell (LDR) [package=THT]
  R9 = Resistor [tolerance=±5% resistance=2.2k package=THT]
  R10 = Resistor [tolerance=±5% resistance=2.2k package=THT]

nets:
  N1: C1.-, Q1.E, M1.pin_2
  N2: C1.+, M1.pin_1, C2.+, M2.pin_1, Part1.5V, R3.Pin_0, R6.Pin_0, R7.Pin_1, R10.Pin_1
  N3: Q1.B, R1.Pin_1
  N4: Q1.C, Q2.C, Part1.GND, LED1.cathode, R5.Pin_1, LED2.cathode, R9.Pin_0
  N5: R1.Pin_0, Part1.D12/MISO
  N6: C2.-, Q2.E, M2.pin_2
  N7: Q2.B, R2.Pin_0
  N8: R2.Pin_1, Part1.D11_PWM/MOSI
  N9: Part1.A3, R8.pin_1, R10.Pin_0
  N10: Part1.A4/SDA, R4.pin_0, R6.Pin_1
  N11: R3.Pin_1, LED1.anode
  N12: R4.pin_1, R5.Pin_0
  N13: LED2.anode, R7.Pin_0
  N14: R8.pin_0, R9.Pin_1

notes:
  Right Side
  Left Side
  Front
  Back
  I connected motors to supply 5V as the motors i used are 4.5 VDC rated.
  You can use another motors. If you connect Arduino by 9V Battery, you can use motors 9V rated and connect them to Vin Power Pin.
