# Fritzing sketch id2437_ardumoto_LFR_0 (saved by Fritzing 0.9.0b)
breadboards: 1

parts:
  Part1 = Arduino Motor Shield
  M1 = DC Motor
  M2 = DC Motor
  Part2 = Arduino Uno (Rev3)  # not connected
  R1 = Photocell (LDR) [package=THT]
  R2 = Resistor [tolerance=±5% resistance=220 package=THT]
  LED1 = LED - 5mm [color="White (6500K)" package="5 mm [THT]"]
  R3 = Resistor [tolerance=±5% resistance=1k package=THT]
  R4 = Resistor [tolerance=±5% resistance=220 package=THT]
  R5 = Resistor [tolerance=±5% resistance=220 package=THT]
  R6 = Resistor [tolerance=±5% resistance=220 package=THT]
  R7 = Resistor [tolerance=±5% resistance=1k package=THT]
  R8 = Resistor [tolerance=±5% resistance=1k package=THT]
  LED2 = LED - 5mm [color="White (6500K)" package="5 mm [THT]"]
  LED3 = LED - 5mm [color="White (6500K)" package="5 mm [THT]"]
  LED4 = LED - 5mm [color="White (6500K)" package="5 mm [THT]"]
  R9 = Photocell (LDR) [package=THT]
  R10 = Photocell (LDR) [package=THT]

nets:
  N1: Part1.OUT3, M1.pin_2
  N2: Part1.OUT4, M1.pin_1
  N3: Part1.OUT2, M2.pin_2
  N4: Part1.OUT1, M2.pin_1
  N5: Part1.5V, R3.Pin_0, R7.Pin_0, R8.Pin_0
  N6: Part1.A0, R8.Pin_1, R10.pin_0
  N7: Part1.A1, R7.Pin_1, R9.pin_0
  N8: Part1.A2, R1.pin_0, R3.Pin_1
  N9: Part1.D9, LED1.anode, LED2.anode, LED3.anode, LED4.anode
  N10: Part1.GND, R1.pin_1, R2.Pin_1, R4.Pin_1, R5.Pin_1, R6.Pin_1, R9.pin_1, R10.pin_1
  N11: R2.Pin_0, LED1.cathode
  N12: R4.Pin_0, LED2.cathode
  N13: R5.Pin_0, LED3.cathode
  N14: R6.Pin_0, LED4.cathode
