# Fritzing sketch id2438_LDR_based_line_following_robot_0 (saved by Fritzing 0.7.4b)
breadboards: 1

parts:
  Part1 = Arduino Motor Shield
  M1 = DC Motor
  M2 = DC Motor
  LED1 = LED - 5mm [color="White (8000K)" package="5 mm [THT]"]
  R2 = Photocell (LDR) [package=THT]
  R3 = Resistor [tolerance=±5% resistance=1k package=THT]
  LED2 = LED - 5mm [color="White (8000K)" package="5 mm [THT]"]
  R4 = Resistor [tolerance=±5% resistance=1k package=THT]
  R5 = Photocell (LDR) [package=THT]
  LED3 = LED - 5mm [color="White (8000K)" package="5 mm [THT]"]
  R6 = Resistor [tolerance=±5% resistance=1k package=THT]
  R7 = Photocell (LDR) [package=THT]
  LED4 = LED - 5mm [color="White (8000K)" package="5 mm [THT]"]
  R8 = Resistor [tolerance=±5% resistance=220 package=THT]
  R9 = Resistor [tolerance=±5% resistance=220 package=THT]
  R10 = Resistor [tolerance=±5% resistance=220 package=THT]
  R11 = Resistor [tolerance=±5% resistance=220 package=THT]

nets:
  N1: Part1.OUT3, M1.pin_2
  N2: Part1.OUT4, M1.pin_1
  N3: Part1.OUT2, M2.pin_2
  N4: Part1.OUT1, M2.pin_1
  N5: Part1.5V, R3.Pin_1, R4.Pin_1, R6.Pin_1
  N6: Part1.A0, R2.pin_0, R3.Pin_0
  N7: Part1.A1, R4.Pin_0, R5.pin_0
  N8: Part1.A2, R6.Pin_0, R7.pin_0
  N9: Part1.D9, LED1.anode, LED2.anode, LED3.anode, LED4.anode
  N10: LED1.cathode, R8.Pin_1
  N11: R2.pin_1, R7.pin_1, R8.Pin_0, R9.Pin_0, R10.Pin_0, R11.Pin_0
  N12: LED2.cathode, R9.Pin_1
  N13: LED3.cathode, R10.Pin_1
  N14: LED4.cathode, R11.Pin_1
