# Fritzing sketch id243_Schematic_0 (saved by Fritzing 0.9.2b)
breadboards: 1

parts:
  Part1 = Arduino Uno (Rev3)
  AD1 = DDS AD9850

nets:
  N1: Part1.D8, AD1.connector28
  N2: Part1.D9_PWM, AD1.connector29
  N3: Part1.D10_PWM/SS, AD1.connector30
  N4: Part1.D11_PWM/MOSI, AD1.connector31
  N5: Part1.5V, AD1.connector14
  N6: Part1.GND, AD1.connector26
