# Fritzing sketch id2441_casa_0 (saved by Fritzing 0.9.2b)
breadboards: 1

parts:
  Componente1 = Arduino Uno (Rev3)
  R1 = Resistor [tolerance=±5% resistance=220 package=THT]
  R2 = Resistor [tolerance=±5% resistance=220 package=THT]
  Q1 = NPN-Transistor [package="TO92 [THT]"]
  R3 = Photocell (LDR) [package=THT]
  R4 = Resistor [tolerance=±5% resistance=220 package=THT]
  LED1 = LED - 5mm [color="Red (633nm)" package="5 mm [THT]"]
  R5 = Rotary Potentiometer (Small) [maximum_resistance=100kΩ package=THT]
  S1 = Toggle Switch [package=THT]
  J1 = Piezo Speaker
  VCC1 = Battery
  LED2 = LED - 5mm [color="Red (633nm)" package="5 mm [THT]"]

nets:
  N1: Componente1.A0, R3.pin_0, R4.Pin_1
  N2: Componente1.A1, S1.COM
  N3: Componente1.D9_PWM, LED1.cathode
  N4: Componente1.D3_PWM, R5.wiper
  N5: Componente1.D5_PWM, R2.Pin_1
  N6: Componente1.5V, R3.pin_1, S1.L1
  N7: Componente1.GND, R1.Pin_0, Q1.E, R4.Pin_0, S1.L2, J1.pin1, VCC1.-
  N8: R1.Pin_1, LED1.anode
  N9: R2.Pin_0, Q1.B
  N10: R5.leg1, J1.pin2
  N11: VCC1.+, LED2.cathode
