# Fritzing sketch id2442_Livello_Acqua_Zapp_0 (saved by Fritzing 0.9.3b)
circuit board: 7.77523cm x 5.55977cm
breadboards: 2

parts:
  J1 = Camdenboss CTB0158-3 [part_number=CTB0158-3 package=THT]
  U1 = 555 Timer [package="DIP8 [THT]"]
  Q1 = NPN-Transistor [part_number=BC548 package="TO92 [THT]"]
  D1 = Diode [part_number=1n4007 package=diode-1n4001]
  R1 = Resistor [tolerance=±5% resistance=100 package=THT]
  R2 = Resistor [tolerance=±5% resistance=100 package=THT]
  R3 = Resistor [tolerance=±5% resistance=10k package=THT]
  R4 = Resistor [tolerance=±5% resistance=250 package=THT]
  J2 = Camdenboss CTB0158-4 [part_number=CTB0158-4 package=THT]
  6V_CC = Power plug
  C1 = Ceramic Capacitor [capacitance=10nF package="0603 [SMD, multilayer]"]
  RELAY_6V = OMRON PCB Power Relay – G5LE [part_number="G5LE-1\n" package=THT]
  Q2 = NPN-Transistor [package="TO92 [THT]"]

nets:
  N1: J1.pin1, R1.Pin_0
  N2: J1.pin2, U1.Trigger, R4.Pin_1
  N3: J1.pin3, U1.Vcc_Supply_Voltage, D1.C, R3.Pin_0, 6V_CC.VCC, RELAY_6V.COIL2
  N4: U1.Ground, U1.Threshold, Q1.E, R4.Pin_0, 6V_CC.GND, C1.1, Q2.E
  N5: U1.Output, R2.Pin_0
  N6: U1.Reset, R3.Pin_1, Q2.C
  N7: U1.Control_Voltage, C1.0
  N8: Q1.B, R2.Pin_1
  N9: Q1.C, D1.A, RELAY_6V.COIL1
  N10: R1.Pin_1, Q2.B
  N11: J2.pin1, RELAY_6V.C
  N12: J2.pin2, J2.pin3
  N13: J2.pin4, RELAY_6V.B
