# Fritzing sketch id2443_skech2_0 (saved by Fritzing 0.9.3b)

parts:
  Componente1 = Arduino Mega 2560 (Rev3)
  U1 = NodeMCUv3 Lolin
  R1 = Resistor [tolerance=±5% resistance=150 package="2512 [SMD]"]
  Q1 = PHOTOTRANSISTOR REFLECTIVE OBJECT SENSOR [package=qrb1114-side]
  Q2 = PHOTOTRANSISTOR REFLECTIVE OBJECT SENSOR [package=qrb1114-side]
  Q3 = PHOTOTRANSISTOR REFLECTIVE OBJECT SENSOR [package=qrb1114-side]
  Q4 = PHOTOTRANSISTOR REFLECTIVE OBJECT SENSOR [package=qrb1114-side]
  Q5 = PHOTOTRANSISTOR REFLECTIVE OBJECT SENSOR [package=qrb1114-side]
  Q6 = PHOTOTRANSISTOR REFLECTIVE OBJECT SENSOR [package=qrb1114-side]
  Q7 = PHOTOTRANSISTOR REFLECTIVE OBJECT SENSOR [package=qrb1114-side]
  Q8 = PHOTOTRANSISTOR REFLECTIVE OBJECT SENSOR [package=qrb1114-side]
  Q9 = PHOTOTRANSISTOR REFLECTIVE OBJECT SENSOR [package=qrb1114-side]
  Q10 = PHOTOTRANSISTOR REFLECTIVE OBJECT SENSOR [package=qrb1114-side]
  Q11 = PHOTOTRANSISTOR REFLECTIVE OBJECT SENSOR [package=qrb1114-side]
  Q12 = PHOTOTRANSISTOR REFLECTIVE OBJECT SENSOR [package=qrb1114-side]
  Q13 = PHOTOTRANSISTOR REFLECTIVE OBJECT SENSOR [package=qrb1114-side]
  Q14 = PHOTOTRANSISTOR REFLECTIVE OBJECT SENSOR [package=qrb1114-side]
  Q15 = PHOTOTRANSISTOR REFLECTIVE OBJECT SENSOR [package=qrb1114-side]
  Q16 = PHOTOTRANSISTOR REFLECTIVE OBJECT SENSOR [package=qrb1114-side]
  R2 = Resistor [tolerance=±5% resistance=150 package="2512 [SMD]"]
  R3 = Resistor [tolerance=±5% resistance=150 package="2512 [SMD]"]
  R4 = Resistor [tolerance=±5% resistance=3.3k package="2512 [SMD]"]
  R5 = Resistor [tolerance=±5% resistance=150 package="2512 [SMD]"]
  R6 = Resistor [tolerance=±5% resistance=150 package="2512 [SMD]"]
  R7 = Resistor [tolerance=±5% resistance=150 package="2512 [SMD]"]
  R8 = Resistor [tolerance=±5% resistance=150 package="2512 [SMD]"]
  R9 = Resistor [tolerance=±5% resistance=150 package="2512 [SMD]"]
  R10 = Resistor [tolerance=±5% resistance=150 package="2512 [SMD]"]
  R11 = Resistor [tolerance=±5% resistance=150 package="2512 [SMD]"]
  R12 = Resistor [tolerance=±5% resistance=150 package="2512 [SMD]"]
  R13 = Resistor [tolerance=±5% resistance=150 package="2512 [SMD]"]
  R14 = Resistor [tolerance=±5% resistance=150 package="2512 [SMD]"]
  R15 = Resistor [tolerance=±5% resistance=150 package="2512 [SMD]"]
  R16 = Resistor [tolerance=±5% resistance=150 package="2512 [SMD]"]
  R17 = Resistor [tolerance=±5% resistance=3.3k package="2512 [SMD]"]
  ULN2003A_-_Stepper_Driver_Board1 = ULN2003A - Stepper Driver Board
  M1 = Stepper Motor - Unipolar
  ULN2003A_-_Stepper_Driver_Board2 = ULN2003A - Stepper Driver Board
  M2 = Stepper Motor - Unipolar
  M3 = DC Motor
  M4 = DC Motor
  R18 = Resistor [tolerance=±5% resistance=3.3k package="2512 [SMD]"]
  R19 = Resistor [tolerance=±5% resistance=3.3k package="2512 [SMD]"]
  R20 = Resistor [tolerance=±5% resistance=3.3k package="2512 [SMD]"]
  R21 = Resistor [tolerance=±5% resistance=3.3k package="2512 [SMD]"]
  R22 = Resistor [tolerance=±5% resistance=3.3k package="2512 [SMD]"]
  R23 = Resistor [tolerance=±5% resistance=3.3k package="2512 [SMD]"]
  R24 = Resistor [tolerance=±5% resistance=3.3k package="2512 [SMD]"]
  R25 = Resistor [tolerance=±5% resistance=3.3k package="2512 [SMD]"]
  R26 = Resistor [tolerance=±5% resistance=3.3k package="2512 [SMD]"]
  R27 = Resistor [tolerance=±5% resistance=3.3k package="2512 [SMD]"]
  R28 = Resistor [tolerance=±5% resistance=3.3k package="2512 [SMD]"]
  R29 = Resistor [tolerance=±5% resistance=3.3k package="2512 [SMD]"]
  R30 = Resistor [tolerance=±5% resistance=3.3k package="2512 [SMD]"]
  R31 = Resistor [tolerance=±5% resistance=3.3k package="2512 [SMD]"]
  R32 = Resistor [tolerance=±5% resistance=3.3k package="2512 [SMD]"]

nets:
  N1: Componente1.A8, Q5.C, R25.Pin_1
  N2: Componente1.A9, Q6.C, R26.Pin_1
  N3: Componente1.A10, Q8.C, R27.Pin_1
  N4: Componente1.A11, Q9.C, R28.Pin_1
  N5: Componente1.A12, Q10.C, R29.Pin_1
  N6: Componente1.A13, Q14.C, R30.Pin_1
  N7: Componente1.A14, Q16.C, R31.Pin_1
  N8: Componente1.A15, Q15.C, R32.Pin_1
  N9: Componente1.A0, Q13.C, R17.Pin_1
  N10: Componente1.A1, Q12.C, R18.Pin_1
  N11: Componente1.A2, Q11.C, R19.Pin_1
  N12: Componente1.A3, Q7.C, R20.Pin_1
  N13: Componente1.A4, Q2.C, R21.Pin_1
  N14: Componente1.A5, Q1.C, R22.Pin_1
  N15: Componente1.A6, Q3.C, R23.Pin_1
  N16: Componente1.A7, Q4.C, R24.Pin_1
  N17: Componente1.GND, U1.connector13, Q10.E, Q13.K, ULN2003A_-_Stepper_Driver_Board2.connector5, M3.pin_1
  N18: Componente1.3V3, U1.connector14
  N19: Componente1.5V, R17.Pin_0, ULN2003A_-_Stepper_Driver_Board1.connector6
  N20: Componente1.D25, M4.pin_2
  N21: Componente1.D27, M3.pin_2
  N22: Componente1.D30, ULN2003A_-_Stepper_Driver_Board1.connector1
  N23: Componente1.D31, ULN2003A_-_Stepper_Driver_Board1.connector2
  N24: Componente1.D32, ULN2003A_-_Stepper_Driver_Board1.connector4
  N25: Componente1.D33, ULN2003A_-_Stepper_Driver_Board1.connector3
  N26: Componente1.D38, ULN2003A_-_Stepper_Driver_Board2.connector1
  N27: Componente1.D39, ULN2003A_-_Stepper_Driver_Board2.connector2
  N28: Componente1.D40, ULN2003A_-_Stepper_Driver_Board2.connector4
  N29: Componente1.D41, ULN2003A_-_Stepper_Driver_Board2.connector3
  N30: Componente1.D50, U1.connector0
  N31: Componente1.D51, U1.connector1
  N32: Componente1.D52, U1.connector2
  N33: Componente1.D53, U1.connector3
  N34: R1.Pin_0, Q13.A
  N35: Q1.A, R6.Pin_0
  N36: Q2.A, R5.Pin_0
  N37: Q3.A, R7.Pin_0
  N38: Q4.A, R8.Pin_0
  N39: Q5.A, R9.Pin_0
  N40: Q6.A, R10.Pin_0
  N41: Q7.A, R4.Pin_0
  N42: Q8.A, R11.Pin_0
  N43: Q9.A, R12.Pin_0
  N44: Q10.A, R13.Pin_0
  N45: Q11.A, R3.Pin_0
  N46: Q12.A, R2.Pin_0
  N47: Q14.A, R14.Pin_0
  N48: Q15.A, R16.Pin_0
  N49: Q16.A, R15.Pin_0
  N50: ULN2003A_-_Stepper_Driver_Board1.connector15, M1.A
  N51: ULN2003A_-_Stepper_Driver_Board1.connector16, M1.COMMON_1
  N52: ULN2003A_-_Stepper_Driver_Board1.connector17, M1.C
  N53: ULN2003A_-_Stepper_Driver_Board1.connector18, M1.B
  N54: ULN2003A_-_Stepper_Driver_Board1.connector19, M1.COMMON_2
  N55: ULN2003A_-_Stepper_Driver_Board1.connector20, M1.D
  N56: ULN2003A_-_Stepper_Driver_Board2.connector15, M2.A
  N57: ULN2003A_-_Stepper_Driver_Board2.connector16, M2.COMMON_1
  N58: ULN2003A_-_Stepper_Driver_Board2.connector17, M2.C
  N59: ULN2003A_-_Stepper_Driver_Board2.connector18, M2.B
  N60: ULN2003A_-_Stepper_Driver_Board2.connector19, M2.COMMON_2
  N61: ULN2003A_-_Stepper_Driver_Board2.connector20, M2.D
