# Fritzing sketch id2446_RTC_Finale_MEGA_0 (saved by Fritzing 0.9.3b)
circuit board: 19.3121cm x 6.75018cm
breadboards: 1

parts:
  Part1 = Arduino Mega 2560 (Rev3)
  LED14 = LED - 3mm [color="Red (633nm)" package="3 mm [THT]"]
  LED15 = LED - 3mm [color="Red (633nm)" package="3 mm [THT]"]
  LED16 = LED - 3mm [color="Red (633nm)" package="3 mm [THT]"]
  LED17 = LED - 3mm [color="Red (633nm)" package="3 mm [THT]"]
  LED18 = LED - 3mm [color="Red (633nm)" package="3 mm [THT]"]
  LED19 = LED - 3mm [color="Red (633nm)" package="3 mm [THT]"]
  LED20 = LED - 3mm [color="Red (633nm)" package="3 mm [THT]"]
  LED21 = LED - 3mm [color="Red (633nm)" package="3 mm [THT]"]
  LED22 = LED - 3mm [color="Red (633nm)" package="3 mm [THT]"]
  LED23 = LED - 3mm [color="Red (633nm)" package="3 mm [THT]"]
  LED24 = LED - 3mm [color="Red (633nm)" package="3 mm [THT]"]
  R25 = Resistor [tolerance=±5% resistance=220 package=THT]
  R26 = Resistor [tolerance=±5% resistance=220 package=THT]
  R27 = Resistor [tolerance=±5% resistance=220 package=THT]
  R28 = Resistor [tolerance=±5% resistance=220 package=THT]
  R29 = Resistor [tolerance=±5% resistance=220 package=THT]
  R30 = Resistor [tolerance=±5% resistance=220 package=THT]
  R31 = Resistor [tolerance=±5% resistance=220 package=THT]
  R32 = Resistor [tolerance=±5% resistance=220 package=THT]
  R33 = Resistor [tolerance=±5% resistance=220 package=THT]
  R34 = Resistor [tolerance=±5% resistance=220 package=THT]
  R35 = Resistor [tolerance=±5% resistance=220 package=THT]
  R36 = Resistor [tolerance=±5% resistance=220 package=THT]
  Tiny_RTC1 = tinyRTC
  LED13 = LED - 3mm [color="Red (633nm)" package="3 mm [THT]"]

nets:
  N1: Part1.D21/SCL, Tiny_RTC1.connector7
  N2: Part1.D20/SDA, Tiny_RTC1.connector8
  N3: Part1.5V, Tiny_RTC1.connector9
  N4: Part1.GND, LED14.cathode, LED15.cathode, LED16.cathode, LED17.cathode, LED18.cathode, LED19.cathode, LED20.cathode, LED21.cathode, LED22.cathode, LED23.cathode, LED24.cathode, Tiny_RTC1.connector10, LED13.cathode
  N5: Part1.D2_PWM, Tiny_RTC1.connector5
  N6: Part1.D29, R27.Pin_1
  N7: Part1.D31, R30.Pin_1
  N8: Part1.D33, R33.Pin_1
  N9: Part1.D35, R35.Pin_1
  N10: Part1.D37, R36.Pin_1
  N11: Part1.D41, R32.Pin_0
  N12: Part1.D43, R29.Pin_0
  N13: Part1.D45, R26.Pin_0
  N14: Part1.D47, R25.Pin_0
  N15: Part1.D49, R34.Pin_0
  N16: Part1.D51, R31.Pin_0
  N17: Part1.D53, R28.Pin_0
  N18: LED14.anode, R28.Pin_1
  N19: LED15.anode, R26.Pin_1
  N20: LED16.anode, R27.Pin_0
  N21: LED17.anode, R31.Pin_1
  N22: LED18.anode, R34.Pin_1
  N23: LED19.anode, R35.Pin_0
  N24: LED20.anode, R36.Pin_0
  N25: LED21.anode, R30.Pin_0
  N26: LED22.anode, R32.Pin_1
  N27: LED23.anode, R29.Pin_1
  N28: LED24.anode, R33.Pin_0
  N29: R25.Pin_1, LED13.anode
