# Fritzing sketch id2447_lm335_0 (saved by Fritzing 0.8.3b)
circuit board: 16.9333cm x 5.64444cm
breadboards: 1

parts:
  Part1 = Arduino Mega ADK (Rev3)
  R1 = Resistor [tolerance=±5% resistance=220 package="0805 [SMD]"]
  R2 = Rotary Potentiometer (Large) [maximum_resistance=100kΩ package=THT]
  T1 = LM35 Temperature Sensor [package="TO92 [THT]"]

nets:
  N1: Part1.A2, R1.Pin_1, T1.Vout
  GND: Part1.GND, R2.leg1, T1.GND
  N2: Part1.IOREF, Part1.5V, R1.Pin_0, R2.leg2
  N3: R2.wiper, T1.+Vs
