# Fritzing sketch id2448_Termometro_lm35_0 (saved by Fritzing 0.8.5b)
breadboards: 1

parts:
  Parte1 = Arduino Uno (Rev3)
  T2 = LM35 Temperature Sensor [package="TO92 [THT]"]
  T3 = LM35 Temperature Sensor [package="TO92 [THT]"]

nets:
  N1: Parte1.A0, T3.Vout
  N2: Parte1.A1, T2.Vout
  GND: Parte1.GND, T3.GND
  N3: Parte1.5V, T3.+Vs
