# Fritzing sketch id2449_dual_limit_switch_LM393_v005_0 (saved by Fritzing 0.8.3b)
circuit board: 4.32979cm x 3.71591cm
breadboards: 1

parts:
  R2s = Resistor [tolerance=±5% resistance=0 package=THT]
  R3h = Resistor [tolerance=±5% resistance=1M package=THT]
  R4p = Resistor [tolerance=±5% resistance=10k package=THT]
  R5p = Resistor [tolerance=±5% resistance=10k package=THT]
  R6s = Resistor [tolerance=±5% resistance=0 package=THT]
  R7s = Resistor [tolerance=±5% resistance=0 package=THT]
  R8 = Resistor [tolerance=±5% resistance=1k package=THT]
  LED1 = LED - 5mm [color="Red (633nm)" package="5 mm [THT]"]
  R9p = Resistor [tolerance=±5% resistance=10k package=THT]
  R10p = Resistor [tolerance=±5% resistance=10k package=THT]
  R12s = Resistor [tolerance=±5% resistance=0 package=THT]
  LED2 = LED - 5mm [color="Red (633nm)" package="5 mm [THT]"]
  R13 = Resistor [tolerance=±5% resistance=1k package=THT]
  C1 = Ceramic Capacitor [capacitance=100nF voltage=16V package="100 mil [THT, multilayer]"]
  C2 = Electrolytic Capacitor [capacitance=1µF voltage=16V package="100 mil [THT, electrolytic]"]
  R11h = Resistor [tolerance=±5% resistance=1M package=THT]
  LM393 = IC, DIP package, 8 pins [chip_label=LM393]
  J1 = Header 4 [package=molex-1x4_lock]
  J2 = Header 4 [package=molex-1x4_lock]

nets:
  N1: R2s.Pin_0, R12s.Pin_1, LM393.pin6
  GND: R2s.Pin_1, R5p.Pin_1, R7s.Pin_1, R10p.Pin_1, C1.1, C2.-, LM393.pin4, J1.1, J2.1
  N2: R3h.Pin_0, R4p.Pin_1, R5p.Pin_0, LM393.pin3
  N3: R3h.Pin_1, LED1.cathode, LM393.pin1, J1.2, J2.2
  12V: R4p.Pin_0, R6s.Pin_0, R8.Pin_1, R9p.Pin_0, R12s.Pin_0, R13.Pin_1, C1.0, C2.+, LM393.pin8, J1.4, J2.4
  N4: R6s.Pin_1, R7s.Pin_0, LM393.pin2
  N5: R8.Pin_0, LED1.anode
  N6: R9p.Pin_1, R10p.Pin_0, R11h.Pin_1, LM393.pin5
  N7: LED2.cathode, R11h.Pin_0, LM393.pin7, J1.3, J2.3
  N8: LED2.anode, R13.Pin_0

notes:
  LM393 based dual set point controller. Comprehensive details about this circuit are to be found at
  http://arts-tech-creation.blogspot.com/2013/07/dual-limit-switch-lm393-based-designed.html
  Part number
  DN2013m07d28i001
  DN2013m07d28i001, Cinternational / WFTelectronics   ... 99guspuppet  & 99Sayaguma  , v001
  R3 & R11 provide hysteresis & may be removed if hysteresis is not desired. Hysteresis ( 1 ) is approximately the paralled value of R4 & R5 divided by R3. Hysteresis ( 2 ) is approximately the paralled value of R9 & R10 divided by R11.
  Section 1
  R6s & R7s can be resistors or thermistors or diodes or photodiodes or CdS cells , etc. used to create a voltage point based on temperature or other variable such as light intensity or pressure.
  Section 1
  R4p & R5p set a trip point voltage
  Section 2
  R9p & R10p set a trip point voltage
  LM393
  Pin 1 is OUT1
  Pin 2 is IN1-
  Pin3 is IN1+
  Pin 7 is OUT2
  Pin 6 is IN2-
  Pin 5 is IN2+
  Pin 4 is GND
  Pin 8 is V+
  The LEDs limit the upper limit of the trip voltage ( slightly ) ... If a higher trip voltage is desired, the LEDs are replaced by zero ohm resistors.
  This circuit will work with voltages as low as 2V ( not recommended ) up to 36V. Capacitor voltage ratings must be sized to have a safety margin of 20%.
  Section 2
  R2s & R12s can be resistors or thermistors or diodes or photodiodes or CdS cells , etc. used to create a voltage point based on temperature or other variable such as light intensity or pressure.
  wire colors
  GND ==> green
  V+ ==> orange
  INx+ ==> yellow
  INx- ==> pink
  OUTx ==> purple
  p ==> set point
  s ==> sensor
  h ==> hysteresis
  C1 & C2 are filter capacitors to smooth the power supply voltage. Should be located near IC
  Headers J1 & J2 provide
  V+ , OUT1 , OUT2 , GND
  J1 & J2
  pin1 ==> GND
  pin2 ==> OUT1
  pin3 ==> OUT2
  pin4 ==> V+
  Two connectors allow more convenience in connecting power and outputs
  Part number
  DN2013m07d28i001
  R9p & R10p can be replaced by a potentiometer.... a 20K pot is suggested.
  An LM393 has open collector outputs. This means the output can sink current & cannot supply current. See datasheet.
