# Fritzing sketch id2450_LMKBD2_0 (saved by Fritzing 0.9.0b)

parts:
  ATMega32u4 = Arduino Micro (Rev3)
  SMBX = RJ12
  J1 = shrouded pin header, 34 pins [form="♂ (shrouded male)"]

nets:
  N1: ATMega32u4.GND, SMBX.connector0, J1.pin1
  N2: ATMega32u4.D2/SDA, J1.pin17
  N3: ATMega32u4.D3/SCL, J1.pin19
  N4: ATMega32u4.D8_PWM/A8, SMBX.connector3
  N5: ATMega32u4.D9_PWM/A9, SMBX.connector4
  N6: ATMega32u4.D10_PWM/A10, SMBX.connector5
  N7: ATMega32u4.5V, SMBX.connector2, J1.pin8
