# Fritzing sketch id2452_lockbot_v0_1_0 (saved by Fritzing 0.9.1b)
breadboards: 2

parts:
  Raspberry_Pi2 = Raspberry Pi B rev2
  IC2 = MCP23017_I2C_I_O_Expander
  Pi1 = Pi_Cobbler
  Power_plug1 = Power plug
  LED1 = LED - 5mm [color="Red (633nm)" package="5 mm [THT]"]
  LED2 = LED - 5mm [color="Green (560nm)" package="5 mm [THT]"]
  LED3 = LED - 5mm [color="Red (633nm)" package="5 mm [THT]"]  # not connected
  S1 = Pushbutton [package="[THT]"]  # not connected
  R1 = Resistor [tolerance=±5% resistance=220 package=THT]
  R2 = Resistor [tolerance=±5% resistance=220 package=THT]

nets:
  N1: Raspberry_Pi2.GPIO_2, IC2.connector11, Pi1.connector3
  N2: Raspberry_Pi2.GPIO_3, IC2.connector13, Pi1.connector5
  N3: Raspberry_Pi2.GND, Pi1.connector6
  N4: IC2.connector9, IC2.connector18, Power_plug1.VCC
  N5: IC2.connector10, IC2.connector15, IC2.connector16, IC2.connector17, Power_plug1.GND, R1.Pin_0, R2.Pin_0
  N6: LED1.cathode, R1.Pin_1
  N7: LED2.cathode, R2.Pin_1

notes:
  5v from wall wart
  3 pins on relay board
  flashing red, and constant green, status indicators
  12V
