# Fritzing sketch id2454_locker_0 (saved by Fritzing 0.9.2b)

parts:
  Board1 = RFID13.56MHzModule
  Part1 = Arduino Uno (Rev3)
  J1 = Basic Servo

nets:
  N1: Board1.connector3, Part1.3V3
  N2: Board1.connector4, Part1.D9_PWM
  GND: Board1.connector5, Part1.GND, J1.gnd
  N3: Board1.connector6, Part1.D12/MISO
  N4: Board1.connector7, Part1.D11_PWM/MOSI
  N5: Board1.connector8, Part1.D13/SCK
  N6: Board1.connector9, Part1.D10_PWM/SS
  N7: Part1.D7, J1.pulse
  5V: Part1.5V, J1.vcc
