# Fritzing sketch id2455_Logic_tester_PCB_Final_0 (saved by Fritzing 0.9.2b)
circuit board: 6.88566cm x 5.36311cm
breadboards: 1

parts:
  LED1 = LED - 5mm [color="Blue (470nm)" package="5 mm [THT]"]
  S2 = Toggle Switch [package=THT]
  LED3 = LED - 5mm [color="Red (633nm)" package="5 mm [THT]"]
  R2 = Resistor [tolerance=±5% resistance=220 package=THT]
  LED2 = LED - 5mm [color="Red (633nm)" package="5 mm [THT]"]
  VCC1 = Battery
  U1 = SN74LS32N [package="DIP14 [THT]"]
  S3 = Toggle Switch [package=THT]
  LED4 = LED - 5mm [color="Blue (470nm)" package="5 mm [THT]"]
  R4 = Resistor [tolerance=±5% resistance=220 package=THT]
  S4 = Toggle Switch [package=THT]
  R3 = Resistor [tolerance=±5% resistance=220 package=THT]
  LED5 = LED - 5mm [color="Red (633nm)" package="5 mm [THT]"]
  R1 = Resistor [tolerance=±5% resistance=220 package=THT]
  R6 = Resistor [tolerance=±5% resistance=220 package=THT]

nets (from the pcb view):
  N1: LED1.cathode, S2.L2, LED3.cathode, LED2.cathode, VCC1.-, U1.GND, S3.L2, LED4.cathode, S4.L2, LED5.cathode
  N2: LED1.anode, R3.Pin_0
  N3: S2.L1, VCC1.+, U1.Vcc, S3.L1, S4.L1
  N4: S2.COM, R2.Pin_1, U1.1B
  N5: LED3.anode, R2.Pin_0
  N6: LED2.anode, R1.Pin_0
  N7: U1.1A, S3.COM, R1.Pin_1
  N8: U1.1Y, R3.Pin_1
  N9: U1.3Y, R4.Pin_0
  N10: U1.3A, S4.COM, R6.Pin_1
  N11: LED4.anode, R4.Pin_1
  N12: LED5.anode, R6.Pin_0

notes:
  Lucas Skye Folio
  1
  0
