# Fritzing sketch id2457_LogicTest_0 (saved by Fritzing 0.9.3b)
breadboards: 1

parts:
  LED1 = LED - 5mm [color="Red (633nm)" package="5 mm [THT]"]
  Q1 = NPN-Transistor [package="TO92 [THT]"]
  R1 = Resistor [tolerance=±1% resistance=150 package=THT]
  R2 = Resistor [tolerance=±1% resistance=20k package=THT]
  R3 = Resistor [tolerance=±1% resistance=1k package=THT]
  Q2 = NPN-Transistor [package="TO92 [THT]"]
  R4 = Resistor [tolerance=±1% resistance=20k package=THT]
  R5 = Resistor [tolerance=±1% resistance=150 package=THT]
  S1 = Pushbutton [package="[THT]"]
  LED2 = LED - 5mm [color="Red (633nm)" package="5 mm [THT]"]

nets:
  N1: LED1.cathode, Q1.C
  N2: LED1.anode, R1.Pin_0
  N3: Q1.E, Q2.E
  N4: Q1.B, R2.Pin_0
  N5: R1.Pin_1, R3.Pin_1, R5.Pin_1
  N6: R2.Pin_1, R3.Pin_0, Q2.C
  N7: Q2.B, R4.Pin_0
  N8: R4.Pin_1, S1.Pin_3, S1.Pin_4, LED2.cathode
  N9: R5.Pin_0, LED2.anode

notes:
  GND
  +5V
