# Fritzing sketch id2458_shield_0 (saved by Fritzing 0.7.0b)
breadboards: 1

parts:
  ------------------------ = Arduino
  <-Accelerometer = female pin header, 6 pins [form="♀ (female)"]
  Data_Logger = female pin header, 20 pins [form="♀ (female)"]
  Sensor = Photocell (LDR) [package=THT]
  <-Sensor = Photocell (LDR) [package=THT]
  LED1 = LED - 5mm [color="Red (633nm)" package="5 mm [THT]"]
  LED2 = LED - 5mm [color="Red (633nm)" package="5 mm [THT]"]
  <-Sensor_2 = Photocell (LDR) [package=THT]
  GND = female pin header, 2 pins [form="♀ (female)"]

nets:
  N1: ------------------------.GND, <-Accelerometer.pin5, Data_Logger.pin3, LED1.cathode, LED2.cathode, GND.pin1
  N2: ------------------------.D13, ------------------------.D12
  N3: ------------------------.D1TX, Data_Logger.pin1
  N4: ------------------------.D0RX, Data_Logger.pin2
  N5: ------------------------.3V3, <-Accelerometer.pin6
  N6: ------------------------.+5V, Sensor.pin_1, <-Sensor.pin_1, LED1.anode, LED2.anode, <-Sensor_2.pin_1, GND.pin2
  N7: ------------------------.A0, Sensor.pin_0
  N8: ------------------------.A1, <-Sensor.pin_0
  N9: ------------------------.A2, <-Accelerometer.pin4
  N10: ------------------------.A3, <-Accelerometer.pin3
  N11: ------------------------.A4, <-Accelerometer.pin2
  N12: ------------------------.A5, <-Sensor_2.pin_0

notes:
  VCC
  GND
  X
  Y
  Z
  Team Liquid
