# Fritzing sketch id2459_PCB4_0 (saved by Fritzing 0.9.3b)
circuit board: 7.14418cm x 5.88684cm
breadboards: 1

parts:
  Part1 = Arduino Uno (Rev3)
  Q1 = PNP-Transistor [package="TO92 [THT]"]
  Q2 = PNP-Transistor [package="TO92 [THT]"]
  Q3 = NPN-Transistor [package="TO92 [THT]"]
  Q4 = NPN-Transistor [package="TO92 [THT]"]
  D1 = Rectifier Diode [part_number=1N4001 package="300 mil [THT]"]
  D2 = Rectifier Diode [part_number=1N4001 package="300 mil [THT]"]
  D3 = Rectifier Diode [part_number=1N4001 package="300 mil [THT]"]
  D4 = Rectifier Diode [part_number=1N4001 package="300 mil [THT]"]
  R1 = Resistor [tolerance=±5% resistance=220 package=THT]
  R2 = Resistor [tolerance=±5% resistance=220 package=THT]
  R3 = Resistor [tolerance=±5% resistance=220 package=THT]
  R4 = Resistor [tolerance=±5% resistance=220 package=THT]
  J1 = Screw terminal - 2 pins [package=THT]
  J2 = Screw terminal - 2 pins [package=THT]
  J3 = Screw terminal - 2 pins [package=THT]
  R5 = Resistor [tolerance=±5% resistance=220 package=THT]

nets:
  N1: Part1.D11_PWM/MOSI, R1.Pin_1, R3.Pin_1
  N2: Part1.D12/MISO, R2.Pin_0, R4.Pin_1
  N3: Part1.GND, Q3.E, Q4.E, D3.anode, D4.anode, J2.pin1, R5.Pin_0
  N4: Part1.5V, Q1.E, Q2.E, D1.cathode, D2.cathode
  N5: Part1.VIN, J2.pin2
  N6: Q1.B, R1.Pin_0
  N7: Q1.C, Q3.C, D1.anode, D3.cathode, J1.pin2
  N8: Q2.B, R2.Pin_1
  N9: Q2.C, Q4.C, D2.anode, D4.cathode, J1.pin1
  N10: Q3.B, R3.Pin_0
  N11: Q4.B, R4.Pin_0
  N12: J3.pin2, R5.Pin_1
