# Fritzing sketch id245_Feather_Huzzah_8266_Battery_Monitor_0 (saved by Fritzing 0.9.3b)
circuit board: 8.46667cm x 5.64444cm
breadboards: 1

parts:
  Part1 = adafruit [part_number="Adafruit #2821"]
  R1 = Resistor [tolerance=±5% resistance=47k package=THT]
  R2 = Resistor [tolerance=±5% resistance=10k package=THT]
  R3 = Resistor [tolerance=±5% resistance=1M package=THT]
  C7 = Ceramic Capacitor [capacitance=100nF package="100 mil [THT, multilayer]"]

nets:
  N1: Part1.connector52, R3.Pin_0, C7.1
  N2: Part1.connector53, R2.Pin_0, C7.0
  N3: Part1.connector59, R1.Pin_0
  N4: R1.Pin_1, R2.Pin_1, R3.Pin_1

notes:
  C7 and R3 are not necessary, but they smooth the reported values a lot.
  You can try without, just connect ADC between R1 and R2
  This is primarily the work of Mike from Adafruit!
  I just documented everything and added the code example
  see: https://forums.adafruit.com/viewtopic.php?f=57&t=111363
