# Fritzing sketch id2460_Sequencer_0 (saved by Fritzing 0.7.1b)
breadboards: 1

parts:
  S1 = Pushbutton [package=THT]
  J1 = Piezo Speaker
  LED1 = LED - 5mm [color="Red (633nm)" package="5 mm [THT]"]
  R1 = Resistor [tolerance=±5% resistance=220 package=THT]
  S2 = Pushbutton [package=THT]
  LED2 = LED - 5mm [color="Green (570nm)" package="5 mm [THT]"]
  R2 = Resistor [tolerance=±5% resistance=220 package=THT]
  R3 = Rotary Potentiometer (Small) [maximum_resistance=100kΩ]
  Arduino1 = Arduino

nets:
  N1: S1.leg0, LED1.anode, Arduino1.D13
  N2: S1.leg1, J1.pin1, S2.leg0, R3.leg1, Arduino1.+5V
  N3: J1.pin2, Arduino1.D2
  N4: LED1.cathode, R1.Pin_1
  N5: R1.Pin_0, R2.Pin_0, R3.leg2, Arduino1.GND
  N6: S2.leg1, LED2.anode, Arduino1.D12
  N7: LED2.cathode, R2.Pin_1
  N8: R3.wiper, Arduino1.A0
