# Fritzing sketch id2461_loop12leds_0 (saved by Fritzing 0.7.10b)
breadboards: 1

parts:
  Arduino1 = Arduino
  LED1 = Blue smd LED [package="0603 [SMD]"]
  LED2 = white smd LED [package="1206 [SMD]"]
  LED3 = red smd LED [package="1206 [SMD]"]
  LED4 = yellow smd LED [package="1206 [SMD]"]
  LED5 = green smd LED [package="1206 [SMD]"]
  LED6 = white LED - 5mm [package="5 mm [THT]"]
  LED7 = Blue smd LED [package="0805 [SMD]"]
  LED8 = white LED - 5mm [package="5 mm [THT]"]
  LED9 = red smd LED [package="0603 [SMD]"]
  LED10 = green smd LED [package="1206 [SMD]"]
  LED11 = white LED - 5mm [package="5 mm [THT]"]
  LED12 = Blue smd LED [package="0603 [SMD]"]

nets:
  N1: Arduino1.GND, LED1.cathode, LED2.cathode, LED3.cathode, LED4.cathode, LED5.cathode, LED6.cathode, LED7.cathode, LED8.cathode, LED9.cathode, LED10.cathode, LED11.cathode, LED12.cathode
  N2: Arduino1.D13, LED1.anode
  N3: Arduino1.D12, LED2.anode
  N4: Arduino1.D11, LED3.anode
  N5: Arduino1.D10, LED4.anode
  N6: Arduino1.D9, LED5.anode
  N7: Arduino1.D8, LED6.anode
  N8: Arduino1.D7, LED7.anode
  N9: Arduino1.D6, LED8.anode
  N10: Arduino1.D5, LED9.anode
  N11: Arduino1.D4, LED10.anode
  N12: Arduino1.D3, LED11.anode
  N13: Arduino1.D2, LED12.anode
