# Fritzing sketch id2462_tape_recorder_0 (saved by Fritzing 0.3.14b)
breadboards: 3

parts:
  IC1 = RTS0073 Integrated Circuit
  SPKR1 = Loudspeaker
  MIC1 = Microphone
  PB = Pushbutton [package=THT]
  REC = Pushbutton [package=THT]
  C1 = Ceramic Capacitor [package=THT]
  R3 = Resistor [resistance=220k package=THT]
  C2 = Electrolytic Capacitor
  LED1 = Red LED - 5mm
  LED2 = green LED - 5mm
  U1 = Voltage Regulator - 5V [package="TO220 [THT]"]
  Power_plug1 = Power plug
  R1 = 1.5M Ω Resistor
  R2 = 1.2M Ω Resistor

nets:
  N1: IC1.connector0, PB.leg0
  N2: IC1.connector2, REC.leg0
  GND: IC1.connector3, IC1.connector7, PB.leg1, REC.leg1, LED1.cathode, LED2.cathode, U1.GND, Power_plug1.GND
  N3: IC1.connector4, SPKR1.pin1
  N4: IC1.connector5, C1.pin_0, R3.Pin_0
  N5: IC1.connector6, C1.pin_1, R3.Pin_1, C2.connector1
  5V: IC1.connector8, IC1.connector11, IC1.connector12, SPKR1.pin2, MIC1.pin2, C2.connector0, U1.output_voltage, R1.connector1, R2.connector0
  N6: IC1.connector9, R2.connector1
  N7: IC1.connector10, R1.connector0
  N8: IC1.connector13, LED1.anode
  N9: IC1.connector14, LED2.anode
  N10: IC1.connector15, MIC1.pin1
  N11: U1.input_voltage, Power_plug1.VCC
