# Fritzing sketch id2467_LUCES_DEL_PATRULLERO_RAUL_0 (saved by Fritzing 0.9.2b)
breadboards: 1

parts:
  Parte1 = Arduino Uno (Rev3)
  LED1 = LED - 5mm [color="Blue (430nm)" package="5 mm [THT]"]
  R1 = Resistor [tolerance=±5% resistance=220 package=THT]
  S1 = Pushbutton [package="[THT]"]
  LED2 = LED - 5mm [color="Red (633nm)" package="5 mm [THT]"]
  R2 = Resistor [tolerance=±5% resistance=220 package=THT]
  LED3 = LED - 5mm [color="Green (555nm)" package="5 mm [THT]"]
  R3 = Resistor [tolerance=±5% resistance=220 package=THT]

nets:
  N1: Parte1.A1, LED2.anode, R2.Pin_1
  N2: Parte1.A2, S1.Pin_3, S1.Pin_4
  N3: Parte1.D8, LED1.cathode
  N4: LED1.anode, R2.Pin_0
  N5: R1.Pin_0, LED2.cathode
  N6: R1.Pin_1, LED3.anode
  N7: S1.Pin_1, S1.Pin_2, R3.Pin_0
