# Fritzing sketch id2472_Untitled_Sketch_0 (saved by Fritzing 0.9.3b)
breadboards: 1

parts:
  LED1 = LED - 5mm [color="Red (633nm)" package="5 mm [THT]"]
  LED3 = LED - 5mm [color="Red (633nm)" package="5 mm [THT]"]
  LED4 = LED - 5mm [color="Red (633nm)" package="5 mm [THT]"]
  LED5 = LED - 5mm [color="Red (633nm)" package="5 mm [THT]"]
  LED6 = LED - 5mm [color="Red (633nm)" package="5 mm [THT]"]
  R2 = Resistor [tolerance=±5% resistance=220 package=THT]
  R7 = Resistor [tolerance=±5% resistance=220 package=THT]
  R8 = Resistor [tolerance=±5% resistance=220 package=THT]
  R9 = Resistor [tolerance=±5% resistance=220 package=THT]
  R10 = Resistor [tolerance=±5% resistance=220 package=THT]
  R11 = Resistor [tolerance=±5% resistance=220 package=THT]
  Componente1 = Arduino Uno (Rev3)
  LED7 = LED - 5mm [color="Red (633nm)" package="5 mm [THT]"]

nets:
  N1: LED1.anode, R9.Pin_0, Componente1.D5_PWM
  N2: LED3.anode, R8.Pin_0, Componente1.D7
  N3: LED4.anode, R7.Pin_0, Componente1.D8
  N4: LED5.anode, R11.Pin_0, Componente1.D4
  N5: LED6.anode, R2.Pin_0, Componente1.D9_PWM
  N6: R2.Pin_1, R8.Pin_1, R9.Pin_1, R10.Pin_1, R11.Pin_1
  N7: R10.Pin_0, Componente1.D6_PWM, LED7.anode
