# Fritzing sketch id2473_focos_led_con_zumbador_e.romero_0 (saved by Fritzing 0.9.3b)
breadboards: 1

parts:
  Componente1 = Arduino Uno (Rev3)
  R1 = Resistor [tolerance=±5% resistance=220 package=THT]
  R2 = Resistor [tolerance=±5% resistance=220 package=THT]
  R3 = Resistor [tolerance=±5% resistance=220 package=THT]
  LED1 = LED - 5mm [color="Red (633nm)" package="5 mm [THT]"]
  LED2 = LED - 5mm [color="Green (570nm)" package="5 mm [THT]"]
  LED3 = LED - 5mm [color="Yellow (595nm)" package="5 mm [THT]"]
  J1 = Piezo Speaker

nets:
  N1: Componente1.D8, J1.pin2
  N2: Componente1.D12/MISO, LED2.anode
  N3: Componente1.D13/SCK, LED1.anode
  N4: Componente1.D7, LED3.anode
  N5: Componente1.GND, R1.Pin_1, R2.Pin_1, R3.Pin_1, J1.pin1
  N6: R1.Pin_0, LED1.cathode
  N7: R2.Pin_0, LED2.cathode
  N8: R3.Pin_0, LED3.cathode
