# Fritzing sketch id2478_luces_secuenciales_con_sonido_Sketch_0 (saved by Fritzing 0.9.3b)
breadboards: 1

parts:
  Componente1 = Arduino Uno (Rev3)
  R1 = Resistor [tolerance=±5% resistance=220 package=THT]
  LED1 = LED - 5mm [color="Red (633nm)" package="5 mm [THT]"]
  LED2 = LED - 5mm [color="Red (633nm)" package="5 mm [THT]"]
  LED3 = LED - 5mm [color="Red (633nm)" package="5 mm [THT]"]
  R4 = Resistor [tolerance=±5% resistance=220 package=THT]
  R5 = Resistor [tolerance=±5% resistance=220 package=THT]
  J1 = Piezo Speaker

nets:
  N1: Componente1.D8, J1.pin2
  N2: Componente1.GND, R1.Pin_1, R4.Pin_1, R5.Pin_1, J1.pin1
  N3: Componente1.D3_PWM, LED1.anode
  N4: Componente1.D4, LED2.anode
  N5: Componente1.D5_PWM, LED3.anode
  N6: R1.Pin_0, LED1.cathode
  N7: LED2.cathode, R4.Pin_0
  N8: LED3.cathode, R5.Pin_0
