# Fritzing sketch id2479_LUCES_Y_NOTAS_MUSICALES1_0 (saved by Fritzing 0.9.3b)
breadboards: 1

parts:
  LED2 = LED - 5mm [color="Red (633nm)" package="5 mm [THT]"]
  LED3 = LED - 5mm [color="Red (633nm)" package="5 mm [THT]"]
  LED4 = LED - 5mm [color="Red (633nm)" package="5 mm [THT]"]
  R1 = Resistor [tolerance=±5% resistance=220 package=THT]
  R2 = Resistor [tolerance=±5% resistance=220 package=THT]
  R3 = Resistor [tolerance=±5% resistance=220 package=THT]
  R4 = Resistor [tolerance=±5% resistance=220 package=THT]
  Componente1 = Arduino Uno (Rev3)
  LED5 = LED - 5mm [color="Red (633nm)" package="5 mm [THT]"]
  SPKR1 = Loudspeaker

nets:
  N1: LED2.cathode, R3.Pin_0
  N2: LED2.anode, Componente1.D6_PWM
  N3: LED3.cathode, R2.Pin_0
  N4: LED3.anode, Componente1.D5_PWM
  N5: LED4.cathode, R1.Pin_0
  N6: R1.Pin_1, R2.Pin_1, R3.Pin_1, R4.Pin_1, Componente1.GND, SPKR1.pin1
  N7: R4.Pin_0, LED5.cathode
  N8: Componente1.D7, LED5.anode
