# Fritzing sketch id2480_luckyDoorRBG_0 (saved by Fritzing 0.8.7b)
breadboards: 1

parts:
  LED1 = RGB LED - (4 legs) [package="5 mm [THT]"]
  LED2 = RGB LED - (4 legs) [package="5 mm [THT]"]
  LED3 = RGB LED - (4 legs) [package="5 mm [THT]"]
  R1 = Resistor [tolerance=±5% resistance=220 package=THT]
  R3 = Resistor [tolerance=±5% resistance=220 package=THT]
  S1 = Pushbutton [package="[THT]"]
  S2 = Pushbutton [package="[THT]"]
  S3 = Pushbutton [package="[THT]"]
  R5 = Resistor [tolerance=±5% resistance=10k package=THT]
  R6 = Resistor [tolerance=±5% resistance=10k package=THT]
  Part1 = Arduino Mega ADK (Rev3)
  R7 = Resistor [tolerance=±5% resistance=220 package=THT]
  R8 = Resistor [tolerance=±5% resistance=220 package=THT]
  R9 = Resistor [tolerance=±5% resistance=220 package=THT]
  R10 = Resistor [tolerance=±5% resistance=220 package=THT]
  R11 = Resistor [tolerance=±5% resistance=220 package=THT]
  R12 = Resistor [tolerance=±5% resistance=220 package=THT]
  R13 = Resistor [tolerance=±5% resistance=220 package=THT]
  R14 = Resistor [tolerance=±5% resistance=10k package=THT]

nets:
  N1: LED1.red_cathode, R3.Pin_1
  N2: LED1.common_anode, LED2.common_anode, LED3.common_anode, R5.Pin_1, R6.Pin_1, Part1.GND, R14.Pin_1
  N3: LED1.green_cathode, R8.Pin_1
  N4: LED1.blue_cathode, R9.Pin_1
  N5: LED2.red_cathode, R7.Pin_1
  N6: LED2.green_cathode, R10.Pin_1
  N7: LED2.blue_cathode, R11.Pin_1
  N8: LED3.red_cathode, R1.Pin_1
  N9: LED3.green_cathode, R12.Pin_1
  N10: LED3.blue_cathode, R13.Pin_1
  N11: R1.Pin_0, Part1.D4_PWM
  N12: R3.Pin_0, Part1.D10_PWM
  N13: S1.Pin_1, S1.Pin_2, Part1.D22, R14.Pin_0
  N14: S1.Pin_3, S1.Pin_4, S2.Pin_3, S2.Pin_4, S3.Pin_3, S3.Pin_4, Part1.5V
  N15: S2.Pin_1, S2.Pin_2, R5.Pin_0, Part1.D23
  N16: S3.Pin_1, S3.Pin_2, R6.Pin_0, Part1.D24
  N17: Part1.D9_PWM, R8.Pin_0
  N18: Part1.D8_PWM, R9.Pin_0
  N19: Part1.D2_PWM, R13.Pin_0
  N20: Part1.D3_PWM, R12.Pin_0
  N21: Part1.D5_PWM, R11.Pin_0
  N22: Part1.D6_PWM, R10.Pin_0
  N23: Part1.D7_PWM, R7.Pin_0
