# Fritzing sketch id2481_Miniprojeto12_Aula8_0 (saved by Fritzing 0.9.3b)
breadboards: 1

parts:
  Componente1 = Arduino Leonardo (Rev3b)
  Componente2 = Bluetooth HC-05 Macho
  R1 = Resistor [tolerance=±5% resistance=330 package="0805 [SMD]"]
  R2 = Resistor [tolerance=±5% resistance=330 package="0805 [SMD]"]
  DHT1 = DHT11_Temperature_and_Humitidy_Sensor
  R3 = Photocell (LDR) [package=THT]
  R4 = Resistor [tolerance=±5% resistance=10k package=THT]

nets:
  N1: Componente1.D0/RX, Componente2.TXD
  N2: Componente1.D1/TX, R2.Pin_1
  5V: Componente1.5V, Componente2.VCC, DHT1.connector1, R3.pin_0
  GND: Componente1.GND, Componente2.GND, R1.Pin_0, DHT1.connector4, R4.Pin_1
  N3: Componente1.A0, R3.pin_1, R4.Pin_0
  N4: Componente1.A5, DHT1.connector2
  N5: Componente2.RXD, R1.Pin_1, R2.Pin_0
