# Fritzing sketch id2482_lunokhod_0 (saved by Fritzing 0.9.0b)

parts:
  Part1 = Arduino Motor Shield (Rev3)
  Part2 = Arduino Mega ADK (Rev3)
  U1 = LCD_CFAX [package=lcd_cfax]
  M1 = DC Motor
  M2 = DC Motor
  U2 = LIPO-2000mAh [package=lipo-2000]
  LED1 = RGB LED (com. cathode, rgb) [package="5 mm [THT]"]

nets:
  N1: Part1.GND, U1.D0, U2.-
  N2: Part1.B-, M2.pin_1
  N3: Part1.B+, M2.pin_2
  N4: Part1.A-, M1.pin_1
  N5: Part1.A+, M1.pin_2
  N6: Part1.VMOT, U2.+
  N7: Part2.D19/RX1, U1.D2
  N8: Part2.D18/TX1, U1.D1
  N9: Part2.D49, LED1.common_cathode
  N10: Part2.D51/MOSI, LED1.green_anode
  N11: Part2.D53/SS, LED1.blue_anode
  N12: Part2.GND, LED1.red_anode
