# Fritzing sketch id2483_Lux_0 (saved by Fritzing 0.7.4b)
breadboards: 1

parts:
  IC1 = IC, DIP package, 8 pins [chip_label=IC spacing=300mil]
  R1 = Resistor [tolerance=±5% resistance=220 package=THT]
  R2 = Resistor [tolerance=±5% resistance=220 package=THT]
  LED1 = LED - 5mm [color="Red (633nm)" package="5 mm [THT]"]
  LED2 = LED - 5mm [color="Red (633nm)" package="5 mm [THT]"]
  VCC1 = Battery
  S1 = Toggle Switch [package=THT]

nets:
  N1: IC1.pin1, LED1.cathode, LED2.cathode, VCC1.-
  N2: IC1.pin4, R2.Pin_0
  N3: IC1.pin5, R1.Pin_0
  N4: IC1.pin7, S1.L2
  N5: R1.Pin_1, LED1.anode
  N6: R2.Pin_1, LED2.anode
  N7: VCC1.+, S1.COM

notes:
  LuxDreamer
