# Fritzing sketch id2484_lyskryss_0 (saved by Fritzing 0.7.12b)
breadboards: 1

parts:
  Arduino1 = Arduino
  LED1 = LED - 5mm [color="Green (570nm)" package="5 mm [THT]"]
  R1 = Resistor [tolerance=±5% resistance=220 package=THT]
  S1 = Pushbutton [package="[THT]"]
  R2 = Resistor [tolerance=±5% resistance=220 package=THT]
  R3 = Resistor [tolerance=±5% resistance=220 package=THT]
  R4 = Resistor [tolerance=±5% resistance=220 package=THT]
  R5 = Resistor [tolerance=±5% resistance=220 package=THT]
  LED2 = LED - 5mm [color="Red (633nm)" package="5 mm [THT]"]
  LED3 = LED - 5mm [color="Red (633nm)" package="5 mm [THT]"]
  LED4 = LED - 5mm [color="Yellow (595nm)" package="5 mm [THT]"]
  LED5 = LED - 5mm [color="Green (570nm)" package="5 mm [THT]"]
  R6 = Resistor [tolerance=±5% resistance=1k package=THT]
  J1 = Piezo Speaker

nets:
  N1: Arduino1.D8, J1.pin1
  N2: Arduino1.D7, LED2.anode
  N3: Arduino1.D6, LED5.anode
  N4: Arduino1.D5, LED3.anode
  N5: Arduino1.D4, LED4.anode
  N6: Arduino1.D3, LED1.anode
  N7: Arduino1.D2, S1.Pin_3, S1.Pin_4, R6.Pin_1
  N8: Arduino1.+5V, S1.Pin_1, S1.Pin_2
  N9: Arduino1.GND, R1.Pin_0, R2.Pin_0, R3.Pin_0, R4.Pin_0, R5.Pin_0, R6.Pin_0, J1.pin2
  N10: LED1.cathode, R3.Pin_1
  N11: R1.Pin_1, LED3.cathode
  N12: R2.Pin_1, LED4.cathode
  N13: R4.Pin_1, LED2.cathode
  N14: R5.Pin_1, LED5.cathode
