# Fritzing sketch id2486_Scheme_0 (saved by Fritzing 0.9.3b)

parts:
  Arduino_Nano = Arduino Nano (Rev3.0)
  DS1307 = Real Time Clock Module - DS1307 RTC Breakout Board
  OLED_0_96 = Grove OLED 128x96
  LED1 = LED - 5mm [color="Red (633nm)" package="5 mm [THT]"]
  LED2 = LED - 5mm [color="Green (555nm)" package="5 mm [THT]"]
  S1 = Pushbutton [package="[THT]"]
  IC1 = ULN2003A [package="DIP16 [THT]"]
  MicroSD = MicroSD Card Module
  Light_Sensor = Ambient Light Sensor (TEMT6000 Breakout Board)
  R1 = Resistor [tolerance=±5% resistance=220 package=THT]
  R2 = Resistor [tolerance=±5% resistance=220 package=THT]
  R3 = Resistor [tolerance=±5% resistance=10k package=THT]
  S2 = Pushbutton [package="[THT]"]
  R4 = Resistor [tolerance=±5% resistance=10k package=THT]

nets:
  N1: Arduino_Nano.GND, LED1.cathode, LED2.cathode, IC1.0V, R3.Pin_0, R4.Pin_0
  N2: Arduino_Nano.D2, S1.Pin_3, S1.Pin_4, R3.Pin_1
  N3: Arduino_Nano.D3, Light_Sensor.S
  N4: Arduino_Nano.D4, IC1.In_7
  N5: Arduino_Nano.D5, IC1.In_6
  N6: Arduino_Nano.D6, IC1.In_5
  N7: Arduino_Nano.D7, IC1.In_4
  N8: Arduino_Nano.D8, S2.Pin_4, R4.Pin_1
  N9: Arduino_Nano.D10, MicroSD.CS
  N10: Arduino_Nano.D11/MOSI, MicroSD.MOSI
  N11: Arduino_Nano.D12/MISO, MicroSD.MISO
  VCC: Arduino_Nano.5V, DS1307.5V, OLED_0_96.VCC, S1.Pin_1, S1.Pin_2, IC1.COM_-_Common, MicroSD.VCC, Light_Sensor.VCC, S2.Pin_1, S2.Pin_2
  N12: Arduino_Nano.A5, DS1307.SCL, OLED_0_96.SCL
  N13: Arduino_Nano.A4, DS1307.SDA, OLED_0_96.SDA
  N14: Arduino_Nano.A1, R2.Pin_1
  N15: Arduino_Nano.A0, R1.Pin_1
  N16: Arduino_Nano.D13/SCK, MicroSD.SCK
  N17: DS1307.GND, IC1.Out_6
  N18: OLED_0_96.GND, IC1.Out_5
  N19: LED1.anode, R2.Pin_0
  N20: LED2.anode, R1.Pin_0
  N21: IC1.Out_7, MicroSD.GND
  N22: IC1.Out_4, Light_Sensor.GND
