# Fritzing sketch id2487_macchina_inutile_0 (saved by Fritzing 0.9.3b)
circuit board: 4cm x 4cm
breadboards: 1

parts:
  VCC1 = Battery
  S1 = Toggle Switch [package=THT]
  R1 = Resistor [tolerance=±5% resistance=247k package=THT]
  R2 = Resistor [tolerance=±5% resistance=12.4k package=THT]
  R3 = Resistor [tolerance=±5% resistance=0 package=THT]
  R4 = Resistor [tolerance=±5% resistance=15k package=THT]
  J1 = Basic Servo
  C1 = Ceramic Capacitor [capacitance=100nF package="100 mil [THT, multilayer]"]
  D1 = Rectifier Diode [part_number=1N4001 package="300 mil [THT]"]
  J3 = female pin header, 2 pins [form="♀ (female)"]
  U1 = 555 Timer [package="DIP8 [THT]"]

nets:
  N1: VCC1.connector0, J1.gnd, C1.1, J3.pin2, U1.Ground
  N2: VCC1.connector1, R2.Pin_0, J1.vcc, J3.pin1, U1.Reset, U1.Vcc_Supply_Voltage
  N3: S1.L1, R3.Pin_0
  N4: S1.COM, R2.Pin_1
  N5: S1.L2, R4.Pin_0
  N6: R1.Pin_0, C1.0, D1.cathode, U1.Trigger, U1.Threshold
  N7: R1.Pin_1, R3.Pin_1, R4.Pin_1, D1.anode, U1.Discharge
  N8: J1.pulse, U1.Output
