# Fritzing sketch id2488_prossesor_machine_0 (saved by Fritzing 0.7.12b)
breadboards: 1

parts:
  IC1 = PICAXE-40X2 [package=THT]
  R1 = 470 Ω Resistor [package=THT]
  S1 = Pushbutton [package="[THT]"]
  J1 = female pin header, 10 pins [form="♀ (female)"]
  J2 = female pin header, 8 pins [form="♀ (female)"]
  J3 = male pin header, 4 pins [form="♂ (male)"]
  J4 = male pin header, 6 pins [form="♂ (male)"]
  J5 = female pin header, 3 pins [form="♀ (female)"]
  XTAL1 = CRYSTAL - kHz [frequency="16 Mhz"]
  J6 = rounded female pin header, 3 pins [form="♀ (female rounded)"]
  J7 = Screw terminal - 2 pins [package=THT]

nets:
  N1: IC1.Reset, R1.Pin_1
  N2: IC1.A.0_/_ADC_0_/_C1-, J3.pin1
  N3: IC1.A.1_/_ADC_1_/_C2-, J3.pin2
  N4: IC1.A.2_/_ADC_2_/_C1+, J3.pin3
  N5: IC1.A.3_/_ADC_3_/_C2+, J3.pin4
  N6: IC1.Serial_In, J5.pin1
  N7: IC1.Serial_Out_/_Out_A.4, J5.pin2
  N8: IC1.A.5_/_ADC_5, J6.pin1
  N9: IC1.A.6_/_ADC_6, J6.pin2
  N10: IC1.A.7_/_ADC_7, J6.pin3
  N11: IC1.+V, R1.Pin_0, S1.Pin_1, S1.Pin_2, S1.Pin_3, S1.Pin_4, J7.pin2
  N12: IC1.0V, J5.pin3, J7.pin1
  N13: IC1.Resonator_(_Optional_)#12, XTAL1.pin_0
  N14: IC1.Resonator_(_Optional_)#13, XTAL1.pin_1
  N15: IC1.C.0_/_Timer_Clock, J4.pin1
  N16: IC1.C.1_/_PWM_C.1, J4.pin2
  N17: IC1.C.2_/_PWM_C.2_/_HPWM_A, J4.pin3
  N18: IC1.C.3_/_I2C_Clock_/_SPI_Clock, J4.pin4
  N19: IC1.D.0, J4.pin5
  N20: IC1.D.1, J4.pin6
  N21: IC1.D.2, J1.pin10
  N22: IC1.D.3, J1.pin9
  N23: IC1.C.4_/_I2C_Data_/_SPI_Data_In, J1.pin8
  N24: IC1.C.5_/_SPI_Data_Out, J1.pin7
  N25: IC1.C.6_/_Hserout, J1.pin6
  N26: IC1.C.7_/_Hserin, J1.pin5
  N27: IC1.D.4, J1.pin4
  N28: IC1.D.5_/_HPWM_C, J1.pin3
  N29: IC1.D.6_/_HPWM_B_/_Keyboard_Clock, J1.pin2
  N30: IC1.D.7_/_HPWM_D_/_Keyboard_Data, J1.pin1
  N31: IC1.B.0, J2.pin8
  N32: IC1.B.1_/_ADC_10_/_Hint_1_/_HPWM_C, J2.pin7
  N33: IC1.B.2_/_ADC_8_/_Hint_2_/_HPWM_B, J2.pin6
  N34: IC1.B.3_/_ADC_9, J2.pin5
  N35: IC1.B.4_/_ADC_11_/_HPWM_D, J2.pin4
  N36: IC1.B.5, J2.pin3
  N37: IC1.B.6, J2.pin2
  N38: IC1.B.7, J2.pin1

notes:
  in data 1
  out data 1
  pcb conection
  pcb conection 2
  w.i.p.
  teeQ
  machine
  processor
  ver. 0.4
