# Fritzing sketch id2489_magiquest_caseta_arduino_light_toggle_0 (saved by Fritzing 0.9.3b)
breadboards: 1

parts:
  Part1 = Arduino Uno (Rev3)
  IR1 = TSOP312.., 314.. [package=THT]
  LED1 = LED - 3mm [color="Green (555nm)" package="3 mm [THT]"]
  LED5 = LED - 3mm [color="Red (633nm)" package="3 mm [THT]"]
  R1 = Resistor [tolerance=±5% resistance=470 package=THT]
  R2 = Resistor [tolerance=±5% resistance=470 package=THT]

nets:
  N1: Part1.D11_PWM/MOSI, IR1.Data
  N2: Part1.D2, LED5.cathode
  N3: Part1.D3_PWM, LED1.cathode
  N4: Part1.3V3, IR1.Vs, R1.Pin_1, R2.Pin_1
  GND: Part1.GND, IR1.GND
  N5: LED1.anode, R1.Pin_0
  N6: LED5.anode, R2.Pin_0
