# Fritzing sketch id248_Firewalker_0 (saved by Fritzing 0.9.2b)

parts:
  FLORA1 = Adafruit_Flora
  NEOPIXEL2 = Neopixel_Strip____White__60_m

nets:
  N1: FLORA1.connector7, NEOPIXEL2.connector4
  N2: FLORA1.connector8, NEOPIXEL2.connector5
  N3: FLORA1.connector10, NEOPIXEL2.connector6

notes:
  Velostat
