# Fritzing sketch id2490_Magnetic_loop_0 (saved by Fritzing 0.9.2b)
circuit board: 8.03491cm x 6.07168cm
breadboards: 1

parts:
  Easydriver = EasyDriver_v44
  L298N_Motor = female alternating pin header, 4 pins [form="♀ (female)"]
  5v_PWR = female pin header, 2 pins [form="♀ (female)"]
  Encoder = female pin header, 5 pins [form="♀ (female)"]
  LED = female pin header, 3 pins [form="♀ (female)"]
  L298N_PWR = female pin header, 2 pins [form="♀ (female)"]
  SW1_Load = female pin header, 2 pins [form="♀ (female)"]
  SG1 = Buzzer 12mm [package=buzzer-12mm-ns]
  Part1 = Arduino Nano (Rev3.0)
  Breakout_Pins = female pin header, 4 pins [form="♀ (female)"]

nets:
  GND: Easydriver.GND, 5v_PWR.pin2, Encoder.pin1, LED.pin2, L298N_PWR.pin2, SW1_Load.pin2, SG1.1, Part1.GND, Breakout_Pins.pin1
  VCC: Easydriver.V+, Easydriver.VCC, 5v_PWR.pin1, L298N_PWR.pin1, Part1.VIN
  N1: Easydriver.STEP, Part1.D9
  N2: Easydriver.DIR, Part1.D8
  N3: Easydriver.OUT2A, L298N_Motor.pin4
  N4: Easydriver.OUT2B, L298N_Motor.pin3
  N5: Easydriver.OUT1A, L298N_Motor.pin2
  N6: Easydriver.OUT1B, L298N_Motor.pin1
  N7: Easydriver.MS1, Part1.D10
  N8: Easydriver.SLEEP, Part1.D12/MISO
  N9: Easydriver.ENABLE, SW1_Load.pin1
  N10: Easydriver.MS2, Part1.D11/MOSI
  N11: Encoder.pin2, Part1.3V3
  N12: Encoder.pin3, Part1.D4
  N13: Encoder.pin4, Part1.D3
  N14: Encoder.pin5, Part1.D2
  N15: LED.pin1, Part1.5V
  N16: LED.pin3, Part1.D5
  N17: SG1.2, Part1.A2, Breakout_Pins.pin4
  N18: Part1.A1, Breakout_Pins.pin3
  N19: Part1.A0, Breakout_Pins.pin2

notes:
  REFER TO DATA SHEET FOR INFORMATION
  L298N PWR 5V
  + VCC
  PWR 5V
  LED
  Nano
  BZ1
  SW1
  Encoder
  Magnetic Loop Controller V1.0 - 12/2015
  Do not remove Easydriver motor wires while powered.
  WARNING-
  +
  GM0OTB
  GND
  5V
  Data
  Load
  CLK
  DT
  SW
  3.3V
  A1
  A2
  B1
  B2
  USB
  Ray Pugh
  PLEASE NOTE!
  [
  GND A0 A1 A2
  Breakout Pins
  Stepper or
  L298N
  Email: ray.pugh@hotmail.co.uk
  Easydriver
