# Fritzing sketch id2492_Mainboard_Schematics_0 (saved by Fritzing 0.9.2b)
breadboards: 1

parts:
  Part1 = Arduino Mega ADK (Rev3)
  Part2 = Compass Module - HMC6352
  Part3 = Logic Level Converter

nets:
  N1: Part1.D21/SCL, Part3.TX_HV
  N2: Part1.D20/SDA, Part3.RX_HV
  GND: Part1.GND, Part2.GND, Part3.GND
  N3: Part1.D52/SCK, Part3.HV
  N4: Part2.VCC, Part3.LV
  N5: Part2.SDA, Part3.RX_LV
  N6: Part2.SCL, Part3.TX_LV
