# Fritzing sketch id2493_majisuripu_0 (saved by Fritzing 0.9.2b)
circuit board: 16cm x 2.4cm
breadboards: 1

parts:
  g = AMPHENOL - ACJS-MHDR [package=ACJS-MHDR]
  y = AMPHENOL - ACJS-MHDR [package=ACJS-MHDR]
  b = connecte
  x = AMPHENOL - ACJS-MHDR [package=ACJS-MHDR]
  r = AMPHENOL - ACJS-MHDR [package=ACJS-MHDR]
  ILDA = F25 [package=db25]

nets:
  GND: g.Sleeve_(1), g.Ring_(2), g.Sleeve_(4), g.Ring_(5), y.Sleeve_(1), y.Sleeve_(4), b.connector0, b.connector1, b.connector3, b.connector4, x.Sleeve_(1), x.Sleeve_(4), r.Sleeve_(1), r.Ring_(2), r.Sleeve_(4), r.Ring_(5), ILDA.25
  N1: g.Tip_(3), g.Tip_(6), ILDA.6
  N2: y.Ring_(2), y.Ring_(5), ILDA.15
  N3: y.Tip_(3), y.Tip_(6), ILDA.2
  N4: b.connector2, b.connector5, ILDA.7
  N5: x.Ring_(2), x.Ring_(5), ILDA.14
  N6: x.Tip_(3), x.Tip_(6), ILDA.1
  N7: r.Tip_(3), r.Tip_(6), ILDA.5
  N8: ILDA.4, ILDA.17

notes:
  jedahan + ⌫
