# Fritzing sketch id2494_Untitled_Sketch_0 (saved by Fritzing 0.9.2b)
breadboards: 1

parts:
  R1 = Resistor [tolerance=±5% resistance=1k package=THT]
  R2_Résistance_inconue = Resistor [tolerance=±5% resistance=220 package=THT]
  Composant1 = Arduino Uno (Rev3)

nets:
  N1: R1.Pin_0, Composant1.GND
  N2: R1.Pin_1, R2_Résistance_inconue.Pin_0, Composant1.A0
  N3: R2_Résistance_inconue.Pin_1, Composant1.5V
