# Fritzing sketch id2495_555_002_0 (saved by Fritzing 0.9.3b)
circuit board: 10cm x 5cm
breadboards: 1

parts:
  U1 = 555 Timer [package="DIP8 [THT]"]
  P1 = POT [package=alps_pot]
  R1 = Resistor [tolerance=±5% resistance=1M package=THT]
  R3 = Resistor [tolerance=±5% resistance=1M package=THT]
  R2 = Resistor [tolerance=±5% resistance=1M package=THT]
  + = male pin header, 1 pin [form="♂ (male)"]
  - = male pin header, 1 pin [form="♂ (male)"]
  R4 = Resistor [tolerance=±5% resistance=1M package=THT]
  C2 = Ceramic Capacitor [capacitance=100nF package="100 mil [THT, multilayer]"]
  C1 = Tantalum Capacitor [capacitance=1μF package="100 mil [THT, tantalum]"]
  C3 = Ceramic Capacitor [capacitance=100nF package="100 mil [THT, multilayer]"]
  D1 = LED - 5mm [color="Red (633nm)" package="5 mm [THT]"]
  R5 = Resistor [tolerance=±5% resistance=1M package=THT]
  C4 = Electrolytic Capacitor [capacitance=0.22mF package="200 mil [THT, electrolytic]"]
  pin_3 = male pin header, 2 pins [form="♂ (male)"]
  +_+ = male pin header, 2 pins [form="♂ (male)"]
  out_+ = male pin header, 1 pin [form="♂ (male)"]
  out_- = male pin header, 1 pin [form="♂ (male)"]
  Q1 = NPN-Transistor [package="TO92 [THT]"]
  Q2 = npn-Powertransistor [package="TO220 [THT]"]
  Q3 = Basic FET N-Channel [package="TO220 [THT]"]  # not connected

nets:
  N1: U1.Ground, -.pin1, C2.0, C1.-, C3.0, D1.anode, C4.-, Q1.E, Q2.emitter
  N2: U1.Trigger, C2.1
  N3: U1.Output, R4.Pin_1, R5.Pin_0, pin_3.pin1, pin_3.pin2
  N4: U1.Reset, U1.Vcc_Supply_Voltage, R1.Pin_1, +.pin1, C4.+, +_+.pin1, +_+.pin2, out_+.pin1
  N5: U1.Control_Voltage, C3.1
  N6: U1.Threshold, P1.S, P1.A, R3.Pin_0, R2.Pin_1
  N7: U1.Discharge, R1.Pin_0, R3.Pin_1
  N8: P1.E, R2.Pin_0, C1.+
  N9: R4.Pin_0, D1.cathode
  N10: R5.Pin_1, Q1.B, Q2.base
  N11: out_-.pin1, Q1.C, Q2.collector

notes:
  http://www.talkingelectronics.com/projects/555 Circuit - Make Any/Make Any 555 Circuit.html
  Talking Electronics - Make any 555
  Circuit
  http://forum.fritzing.org.com/ Make Any 555
