# Fritzing sketch id2497_Untitled_Sketch_0 (saved by Fritzing 0.9.1b)

parts:
  Composant1 = Arduino Uno (Rev3)
  R1 = Rotary Potentiometer (Small) [maximum_resistance=100kΩ package=THT]
  J1 = Basic Servo

nets:
  N1: Composant1.A0, R1.wiper
  GND: Composant1.GND, R1.leg1, J1.gnd
  N2: Composant1.D2, J1.pulse
  N3: R1.leg2, J1.vcc

notes:
  Titouan VINCENT
