# Fritzing sketch id2498_ARDUINOBREADBOARDTUTORIAL_0 (saved by Fritzing 0.3.14b)
breadboards: 6

parts:
  VCC1 = obsolete Battery
  S1 = Pushbutton [package="[THT]"]
  C1 = Electrolytic Capacitor [package=THT]
  U1 = Voltage Regulator - 5V [package="TO220 [THT]"]
  C2 = Electrolytic Capacitor [package=THT]
  R1 = Resistor [resistance=220 package=THT]
  LED1 = Red LED - 5mm
  VCC2 = obsolete Battery
  VCC3 = obsolete Battery
  U2 = atmega168 [package="DIP28 [THT]"]
  R2 = Resistor [resistance=10k package=THT]
  XTAL1 = Crystal [package=THT]
  C3 = Ceramic Disk Capacitor [package=THT]
  C3_2 = Ceramic Disk Capacitor [package=THT]
  CONN2 = USB connector [package=THT]
  LED4 = Blue LED - 5mm
  LED5 = Red LED - 5mm
  LED6 = green LED - 5mm
  R3 = Resistor [resistance=220 package=THT]
  J1 = female pin header, 6 pins [form="♀ (female)"]
  J2 = female pin header, 14 pins [form="♀ (female)"]
  VCC4 = obsolete Battery  # not connected
  VCC5 = obsolete Battery  # not connected
  VCC6 = obsolete Battery  # not connected
  VCC4_2 = obsolete Battery
  VCC5_2 = obsolete Battery
  VCC6_2 = obsolete Battery
  VCC4_3 = obsolete Battery
  VCC5_3 = obsolete Battery
  VCC6_3 = obsolete Battery
  U3 = Voltage Regulator - 5V [package="TO220 [THT]"]
  C4 = Electrolytic Capacitor [package=THT]
  C4_2 = Electrolytic Capacitor [package=THT]
  VCC4_4 = obsolete Battery
  VCC5_4 = obsolete Battery
  VCC6_4 = obsolete Battery
  U3_2 = Voltage Regulator - 5V [package="TO220 [THT]"]
  C4_3 = Electrolytic Capacitor [package=THT]
  C4_4 = Electrolytic Capacitor [package=THT]
  LED7 = Red LED - 5mm
  R4 = Resistor [resistance=220 package=THT]
  VCC4_5 = obsolete Battery
  VCC5_5 = obsolete Battery
  VCC6_5 = obsolete Battery
  U3_3 = Voltage Regulator - 5V [package="TO220 [THT]"]
  C4_5 = Electrolytic Capacitor [package=THT]
  C4_6 = Electrolytic Capacitor [package=THT]
  LED7_2 = Red LED - 5mm
  R4_2 = Resistor [resistance=220 package=THT]
  U4 = atmega168 [package="DIP28 [THT]"]
  R5 = Resistor [resistance=10k package=THT]

nets:
  N1: VCC1.-, VCC2.+
  N2: VCC1.+, VCC3.-
  N3: S1.Pin_1, S1.Pin_2, C1.-, U1.GND, C2.-, R1.Pin_0, VCC2.-, U2.Pin_8, U2.Pin_22, C3.pin_0, C3_2.pin_0
  N4: S1.Pin_3, S1.Pin_4, U2.Pin_1, R2.Pin_1
  N5: C1.+, U1.input_voltage, VCC3.+, U2.Pin_20, U2.Pin_21
  N6: U1.output_voltage, C2.+
  N7: R1.Pin_1, LED1.anode
  N8: LED1.cathode, U2.Pin_7, R2.Pin_0
  N9: U2.Pin_2, LED5.cathode, J2.pin14
  N10: U2.Pin_3, LED4.anode, J2.pin13
  N11: U2.Pin_4, J2.pin12
  N12: U2.Pin_5, J2.pin11
  N13: U2.Pin_6, J2.pin10
  N14: U2.Pin_9, XTAL1.pin_0, C3_2.pin_1
  N15: U2.Pin_10, XTAL1.pin_1, C3.pin_1
  N16: U2.Pin_11, J2.pin9
  N17: U2.Pin_12, J2.pin8
  N18: U2.Pin_13, J2.pin7
  N19: U2.Pin_14, J2.pin6
  N20: U2.Pin_15, J2.pin5
  N21: U2.Pin_16, J2.pin4
  N22: U2.Pin_17, J2.pin3
  N23: U2.Pin_18, J2.pin2
  N24: U2.Pin_19, LED6.anode
  N25: U2.Pin_23, J1.pin6
  N26: U2.Pin_24, J1.pin5
  N27: U2.Pin_25, J1.pin4
  N28: U2.Pin_26, J1.pin3
  N29: U2.Pin_27, J1.pin2
  N30: U2.Pin_28, J1.pin1
  N31: CONN2.d-, LED4.cathode
  N32: CONN2.d+, LED5.anode
  N33: LED6.cathode, R3.Pin_1
  N34: R3.Pin_0, J2.pin1
  N35: VCC4_2.+, VCC5_2.-
  N36: VCC5_2.+, VCC6_2.-
  N37: VCC4_3.-, U3.GND, C4.-, C4_2.-
  N38: VCC4_3.+, VCC5_3.-
  N39: VCC5_3.+, VCC6_3.-
  N40: VCC6_3.+, U3.input_voltage, C4.+, C4_2.+
  N41: VCC4_4.-, U3_2.GND, C4_3.-, C4_4.-, LED7.cathode
  N42: VCC4_4.+, VCC5_4.-
  N43: VCC5_4.+, VCC6_4.-
  N44: VCC6_4.+, U3_2.input_voltage, C4_3.+, C4_4.+, R4.Pin_0
  N45: LED7.anode, R4.Pin_1
  N46: VCC4_5.-, U3_3.GND, C4_5.-, C4_6.-, LED7_2.cathode, U4.Pin_8, U4.Pin_22
  N47: VCC4_5.+, VCC5_5.-
  N48: VCC5_5.+, VCC6_5.-
  N49: VCC6_5.+, U3_3.input_voltage, C4_5.+, C4_6.+, R4_2.Pin_0, U4.Pin_7, U4.Pin_20, U4.Pin_21, R5.Pin_0
  N50: LED7_2.anode, R4_2.Pin_1
  N51: U4.Pin_1, R5.Pin_1

notes:
  BUILD YOUR OWN ARDUINO DECIMILIA
  This step-by-step tutorial was created by Newprofile001.
  SCROLL OVER TO CONTINUE ►
  GET OUT 3 FULL BATTERY PACKS AND A FULL BREADBOARD.
  WE COULD USE A 9V BUT IT DOESN'T LAST AS LONG AS 6 AA BATTERIES.
  GET THIS!
  Did you know that a 9V battery is just 6 AAAA batteries (that's 4 "A"s) hooked in series?
  HOOK BATTERIES IN SERIES AND CONNECT TO THE TOP RAIL. WIRE RAILS TOGETHER.
  For your convenience, the wires are color-coded according to use:
  Black: Negative, safe voltage.
  Red: Positive, safe voltage.
  White: Negative, dangerous voltage.
  Grey: EITHER battery series connection OR positive, dangerous voltage.
  Green: Fault-to-ground line. REMEMBER WHERE IT WAS.
  Blue: General purpose.
  Orange: IR data
  Yellow: Neutral wire.
  I will do this throughout the tutorial. You do not need to do this, but you can if you want to. I do this myself for easier troubleshooting.
  ADD 2 10µF CAPACITORS. ONE GOES BETWEEN POWER AND GROUND.
  THE OTHER GOES BETWEEN THE INPUT AND GROUND LEGS OF THE VOLTAGE REGULATOR.
  NOTE THE LOCATION OF THE BRIGHT STRIP ON THE CAPACITOR - THAT GOES TOWARD GROUND.
  !!! SAFETY ALERT !!!
  CAPACITORS ARE CAPABLE OF HOLDING DANGEROUS VOLTAGES/AMPERAGES. A CURRENT OF .5A IS MORE THAN ENOUGH TO CAUSE CARDIAC ARREST. SHORT THE TERMINALS OF A CAPACITOR WITH A SCREWDRIVER BEFORE HANDLING - THIS DISCHARGES ANY ELECTRICITY THAT MAY BE STORED.
  !!! SAFETY ALERT !!!
  IF THE SIDES OF AN ELECTROLYCTIC CAPACITOR ARE SWOLLEN OR THERE IS A BULGE NEAR THE TERMINALS OF AN ELECTROLYCTIC CAPACITOR, TURN OFF THE CIRCUIT, SHORT THE TERMINALS WITH A SCREWDRIVER, AND REPLACE IT. ALWAYS REPLACE A CAPACITOR WITH THE SAME VOLTAGE AND FARAD RATING.
  ADD LED (NOTE THE FLAT SIDE) AND A 220Ω RESISTOR.
  ADD ATMEGA168 CHIP AND SUPPORTING CIRCUITRY. THIS IS THE END OF THIS TUTORIAL; GO TO "MAKE YOUR OWN ARDUINO PART 2!"
  TUTORIAL FROM http://itp.nyu.edu/physcomp/Tutorials/ArduinoBreadboard .
  For reasons unknown, the Fritzing project thingy ALWAYS makes this the starting view. Hold "PAGE UP", it'll get you there.
