# Fritzing sketch id2499_arduinobreadboardtutorial2_0 (saved by Fritzing 0.3.14b)
breadboards: 6

parts:
  VCC4 = obsolete Battery
  VCC5 = obsolete Battery
  VCC6 = obsolete Battery
  U3 = Voltage Regulator - 5V [package="TO220 [THT]"]
  C4 = Electrolytic Capacitor [package=THT]
  C4_2 = Electrolytic Capacitor [package=THT]
  LED7 = Red LED - 5mm
  R4 = Resistor [resistance=220 package=THT]
  U4 = atmega168 [package="DIP28 [THT]"]
  R5 = Resistor [resistance=10k package=THT]
  VCC4_2 = obsolete Battery
  VCC5_2 = obsolete Battery
  VCC6_2 = obsolete Battery
  U3_2 = Voltage Regulator - 5V [package="TO220 [THT]"]
  C4_3 = Electrolytic Capacitor [package=THT]
  C4_4 = Electrolytic Capacitor [package=THT]
  LED7_2 = Red LED - 5mm
  R4_2 = Resistor [resistance=220 package=THT]
  U4_2 = atmega168 [package="DIP28 [THT]"]
  R5_2 = Resistor [resistance=10k package=THT]
  C5 = Ceramic Disk Capacitor [package=THT]
  C5_2 = Ceramic Disk Capacitor [package=THT]
  XTAL1 = Crystal [package=THT]
  S1 = Pushbutton [package="[THT]"]
  VCC4_3 = obsolete Battery
  VCC5_3 = obsolete Battery
  VCC6_3 = obsolete Battery
  U3_3 = Voltage Regulator - 5V [package="TO220 [THT]"]
  C4_5 = Electrolytic Capacitor [package=THT]
  C4_6 = Electrolytic Capacitor [package=THT]
  LED7_3 = Red LED - 5mm
  R4_3 = Resistor [resistance=220 package=THT]
  U4_3 = atmega168 [package="DIP28 [THT]"]
  R5_3 = Resistor [resistance=10k package=THT]
  C5_3 = Ceramic Disk Capacitor [package=THT]
  C5_4 = Ceramic Disk Capacitor [package=THT]
  XTAL1_2 = Crystal [package=THT]
  S1_2 = Pushbutton [package="[THT]"]
  LED8 = green LED - 5mm
  R6 = Resistor [resistance=220 package=THT]
  VCC4_4 = obsolete Battery
  VCC5_4 = obsolete Battery
  VCC6_4 = obsolete Battery
  U3_4 = Voltage Regulator - 5V [package="TO220 [THT]"]
  C4_7 = Electrolytic Capacitor [package=THT]
  C4_8 = Electrolytic Capacitor [package=THT]
  LED7_4 = Red LED - 5mm
  R4_4 = Resistor [resistance=220 package=THT]
  U4_4 = atmega168 [package="DIP28 [THT]"]
  R5_4 = Resistor [resistance=10k package=THT]
  C5_5 = Ceramic Disk Capacitor [package=THT]
  C5_6 = Ceramic Disk Capacitor [package=THT]
  XTAL1_3 = Crystal [package=THT]
  S1_3 = Pushbutton [package="[THT]"]
  LED8_2 = green LED - 5mm
  R6_2 = Resistor [resistance=220 package=THT]
  CONN1 = USB connector [package=THT]  # not connected
  CONN2 = USB connector [package=THT]
  VCC4_5 = obsolete Battery
  VCC5_5 = obsolete Battery
  VCC6_5 = obsolete Battery
  U3_5 = Voltage Regulator - 5V [package="TO220 [THT]"]
  C4_9 = Electrolytic Capacitor [package=THT]
  C4_10 = Electrolytic Capacitor [package=THT]
  LED7_5 = Red LED - 5mm
  R4_5 = Resistor [resistance=220 package=THT]
  U4_5 = atmega168 [package="DIP28 [THT]"]
  R5_5 = Resistor [resistance=10k package=THT]
  C5_7 = Ceramic Disk Capacitor [package=THT]
  C5_8 = Ceramic Disk Capacitor [package=THT]
  XTAL1_4 = Crystal [package=THT]
  S1_4 = Pushbutton [package="[THT]"]
  LED8_3 = green LED - 5mm
  R6_3 = Resistor [resistance=220 package=THT]
  CONN2_2 = USB connector [package=THT]
  LED9 = yellow LED - 5mm
  LED10 = Blue LED - 5mm
  R7 = Resistor [resistance=220 package=THT]
  R8 = Resistor [resistance=220 package=THT]
  CONN3 = USB connector [package=THT]
  U5 = atmega168 [package="DIP28 [THT]"]
  U6 = atmega168 [package="DIP28 [THT]"]
  Arduino1 = Arduino
  J2 = female pin header, 6 pins [form="♀ (female)"]
  J2_2 = female pin header, 6 pins [form="♀ (female)"]
  J1 = female pin header, 8 pins [form="♀ (female)"]
  J1_2 = female pin header, 8 pins [form="♀ (female)"]
  XTAL2 = Crystal [package=THT]

nets:
  N1: VCC4.-, U3.GND, C4.-, C4_2.-, LED7.cathode, U4.Pin_8, U4.Pin_22
  N2: VCC4.+, VCC5.-
  N3: VCC5.+, VCC6.-
  N4: VCC6.+, U3.input_voltage, C4.+, C4_2.+, R4.Pin_0, U4.Pin_7, U4.Pin_20, U4.Pin_21, R5.Pin_0
  N5: LED7.anode, R4.Pin_1
  N6: U4.Pin_1, R5.Pin_1
  N7: VCC4_2.-, U3_2.GND, C4_3.-, C4_4.-, LED7_2.cathode, U4_2.Pin_8, U4_2.Pin_22, C5.pin_0, C5_2.pin_0, S1.Pin_3, S1.Pin_4
  N8: VCC4_2.+, VCC5_2.-
  N9: VCC5_2.+, VCC6_2.-
  N10: VCC6_2.+, U3_2.input_voltage, C4_3.+, C4_4.+, R4_2.Pin_0, U4_2.Pin_7, U4_2.Pin_20, U4_2.Pin_21, R5_2.Pin_0
  N11: LED7_2.anode, R4_2.Pin_1
  N12: U4_2.Pin_1, R5_2.Pin_1, S1.Pin_1, S1.Pin_2
  N13: U4_2.Pin_9, C5_2.pin_1, XTAL1.pin_0
  N14: U4_2.Pin_10, C5.pin_1, XTAL1.pin_1
  N15: VCC4_3.-, U3_3.GND, C4_5.-, C4_6.-, LED7_3.cathode, U4_3.Pin_8, U4_3.Pin_22, C5_3.pin_0, C5_4.pin_0, S1_2.Pin_3, S1_2.Pin_4, R6.Pin_1
  N16: VCC4_3.+, VCC5_3.-
  N17: VCC5_3.+, VCC6_3.-
  N18: VCC6_3.+, U3_3.input_voltage, C4_5.+, C4_6.+, R4_3.Pin_0, U4_3.Pin_7, U4_3.Pin_20, U4_3.Pin_21, R5_3.Pin_0
  N19: LED7_3.anode, R4_3.Pin_1
  N20: U4_3.Pin_1, R5_3.Pin_1, S1_2.Pin_1, S1_2.Pin_2
  N21: U4_3.Pin_9, C5_4.pin_1, XTAL1_2.pin_0
  N22: U4_3.Pin_10, C5_3.pin_1, XTAL1_2.pin_1
  N23: U4_3.Pin_19, LED8.anode
  N24: LED8.cathode, R6.Pin_0
  GND: VCC4_4.-, U3_4.GND, C4_7.-, C4_8.-, LED7_4.cathode, U4_4.Pin_8, U4_4.Pin_22, C5_5.pin_0, C5_6.pin_0, S1_3.Pin_3, S1_3.Pin_4, R6_2.Pin_1, CONN2.GND
  N25: VCC4_4.+, VCC5_4.-
  N26: VCC5_4.+, VCC6_4.-
  N27: VCC6_4.+, U3_4.input_voltage, C4_7.+, C4_8.+, R4_4.Pin_0, U4_4.Pin_7, U4_4.Pin_20, U4_4.Pin_21, R5_4.Pin_0, CONN2.5V
  N28: LED7_4.anode, R4_4.Pin_1
  N29: U4_4.Pin_1, R5_4.Pin_1, S1_3.Pin_1, S1_3.Pin_2
  N30: U4_4.Pin_9, C5_5.pin_1, XTAL1_3.pin_0
  N31: U4_4.Pin_10, C5_6.pin_1, XTAL1_3.pin_1
  N32: U4_4.Pin_19, LED8_2.anode
  N33: LED8_2.cathode, R6_2.Pin_0
  GND_2: VCC4_5.-, U3_5.GND, C4_9.-, C4_10.-, LED7_5.cathode, U4_5.Pin_8, U4_5.Pin_22, C5_7.pin_0, C5_8.pin_0, S1_4.Pin_3, S1_4.Pin_4, R6_3.Pin_1, CONN2_2.GND
  N34: VCC4_5.+, VCC5_5.-
  N35: VCC5_5.+, VCC6_5.-
  N36: VCC6_5.+, U3_5.input_voltage, C4_9.+, C4_10.+, R4_5.Pin_0, U4_5.Pin_7, U4_5.Pin_20, U4_5.Pin_21, R5_5.Pin_0, CONN2_2.5V
  N37: LED7_5.anode, R4_5.Pin_1
  N38: U4_5.Pin_1, R5_5.Pin_1, S1_4.Pin_1, S1_4.Pin_2
  N39: U4_5.Pin_2, LED9.anode
  N40: U4_5.Pin_3, LED10.cathode
  N41: U4_5.Pin_9, C5_8.pin_1, XTAL1_4.pin_0
  N42: U4_5.Pin_10, C5_7.pin_1, XTAL1_4.pin_1
  N43: U4_5.Pin_19, LED8_3.anode
  N44: LED8_3.cathode, R6_3.Pin_0
  N45: CONN2_2.d-, R8.Pin_1
  N46: CONN2_2.d+, R7.Pin_1
  N47: LED9.cathode, R7.Pin_0
  N48: LED10.anode, R8.Pin_0
  N49: CONN3.d-, U5.Pin_3
  N50: CONN3.d+, U5.Pin_2
  N51: U6.Pin_1, Arduino1.RST, J2_2.pin1
  N52: U6.Pin_2, Arduino1.D0RX, J1_2.pin8
  N53: U6.Pin_3, Arduino1.D1TX, J1_2.pin7
  N54: U6.Pin_4, Arduino1.D2, J1_2.pin6
  N55: U6.Pin_5, Arduino1.D3, J1_2.pin5
  N56: U6.Pin_6, Arduino1.D4, J1_2.pin4
  N57: U6.Pin_7, Arduino1.+5V, J2_2.pin3
  N58: U6.Pin_8, U6.Pin_22, Arduino1.GND, J2_2.pin4, J2_2.pin5, J1.pin2
  N59: U6.Pin_9, XTAL2.pin_0
  N60: U6.Pin_10, XTAL2.pin_1
  N61: U6.Pin_11, Arduino1.D5, J1_2.pin3
  N62: U6.Pin_12, Arduino1.D6, J1_2.pin2
  N63: U6.Pin_13, Arduino1.D7, J1_2.pin1
  N64: U6.Pin_14, Arduino1.D8, J1.pin8
  N65: U6.Pin_15, Arduino1.D9, J1.pin7
  N66: U6.Pin_16, Arduino1.D10, J1.pin6
  N67: U6.Pin_17, Arduino1.D11, J1.pin5
  N68: U6.Pin_18, Arduino1.D12, J1.pin4
  N69: U6.Pin_19, Arduino1.D13, J1.pin3
  N70: U6.Pin_21, Arduino1.aref, J1.pin1
  N71: U6.Pin_23, Arduino1.A0, J2.pin1
  N72: U6.Pin_24, Arduino1.A1, J2.pin2
  N73: U6.Pin_25, Arduino1.A2, J2.pin3
  N74: U6.Pin_26, Arduino1.A3, J2.pin4
  N75: U6.Pin_27, Arduino1.A4, J2.pin5
  N76: U6.Pin_28, Arduino1.A5, J2.pin6
  N77: Arduino1.3V3, J2_2.pin2
  N78: Arduino1.VIN, J2_2.pin6

notes:
  BUILD YOUR OWN ARDUINO DECIMILIA, PART 2
  BY NEWPROFILE001
  TUTORIAL IS AT http://itp.nyu.edu/physcomp/Tutorials/ArduinoBreadboard
  SO FAR WE SHOULD HAVE THIS. IF YOU DON'T, YOU MUST HAVE SKIPPED A STEP. WE ADD MORE THINGS OVER THERE TO THE RIGHT.
  ADD A 16mHz CLOCK AND 2 22pF CERAMIC CAPACITORS BETWEEN PINS 9 AND 10 AND A RESET BUTTON NOW. YOU CAN USE A 4-PIN OR A 2-PIN, BUT A 4-PIN IS EASIER FOR ME.
  ADD A LED AND A 220Ω RESISTOR TO GROUND. LED WIRE GOES TO PIN 19.
  NOW WE GET COMPLICATED. TAKE A USB CONNECTOR - LIKE THIS:
  AND PUT IT ON THE END IN THE MIDDLE.
  HERE IT LOOKS LIKE ONE BLACK WIRE, BUT IT IS TWO. ONE HEADS TO THE TOP RAIL FROM THE BOTTOM RAIL, AND THE OTHER LEADS TO THE USB CONNECTOR FROM THE TOP RAIL.
  OPTIONAL:
  ADD 2 LEDS WITH THE FLAT SIDES RIGHT BESIDE EACH OTHER AND 2 220Ω RESISTORS. WIRE TO PIN 2 AND 3 AS SHOWN. IF THE LEDs DO NOT LIGHT OR DATA IS NOT SENDING/RECEIVING, ROTATE THE YELLOW AND BLUE LEDs.
  IF YOU DID NOT DO THE OPTIONAL STEP, CONNECT THE USB LOWER PINS TO THE ATMEGA168 LIKE THIS:
  HERE I WIRED THE ATMEGA168'S PINS AS WE SEE THEM ON THE ARDUINO DECIMILIA.
  THIS IS THE END OF THE TUTORIAL, BUT AS AN ADDED BONUS YOU CAN SEE THE ARDUINO DECIMILIA WIRED WITH THE ATMEGA168 CONTROLLER OVER TO THE RIGHT.
  Alright. Move over to the left...
  ...and move up.
