# Fritzing sketch id249_Huzah_DS18B20_parasite_power_0 (saved by Fritzing 0.9.2b)
breadboards: 1

parts:
  Adafruit_HUZZAH_ESP8266_Breakout = Adafruit HUZZAH ESP8266 Breakout [part_number=2471]
  DS1 = pkutans [part_number=DS18B20]
  R1 = Resistor [tolerance=±5% resistance=1k package=THT]

nets:
  N1: Adafruit_HUZZAH_ESP8266_Breakout.GND, DS1.connector1, DS1.connector3
  N2: Adafruit_HUZZAH_ESP8266_Breakout.#14, DS1.connector2, R1.Pin_1
  N3: Adafruit_HUZZAH_ESP8266_Breakout.3V, R1.Pin_0

notes:
  DS18B20 in parasite power mode:
  External pull up: 1k Ohm
