# Fritzing sketch id2500_Millis_Example_0 (saved by Fritzing 0.9.3b)
breadboards: 1

parts:
  U1 = NodeMCUv3 Lolin
  LED1 = LED - 5mm [color="Red (633nm)" package="5 mm [THT]"]
  LED2 = LED - 5mm [color="Green (560nm)" package="5 mm [THT]"]

nets:
  N1: U1.connector3, LED1.anode
  N2: U1.connector4, LED2.cathode
  N3: U1.connector13, LED1.cathode, LED2.anode
