# Fritzing sketch id2501_Manage_3_LEDs_with_2_push_buttons_0 (saved by Fritzing 0.9.1b)
breadboards: 1

parts:
  Componente1 = Arduino Uno (Rev3)
  LED1 = LED - 5mm [color="Red (633nm)" package="5 mm [THT]"]
  LED2 = LED - 5mm [color="Yellow (595nm)" package="5 mm [THT]"]
  LED3 = LED - 5mm [color="Green (555nm)" package="5 mm [THT]"]
  R1 = Resistor [tolerance=±5% resistance=220 package=THT]
  S1 = Pushbutton [package="[THT]"]
  S2 = Pushbutton [package="[THT]"]
  R2 = Resistor [tolerance=±5% resistance=10k package=THT]
  R3 = Resistor [tolerance=±5% resistance=10k package=THT]

nets:
  N1: Componente1.D11_PWM/MOSI, LED1.anode
  N2: Componente1.D12/MISO, LED2.anode
  N3: Componente1.D13/SCK, LED3.anode
  N4: Componente1.GND, R1.Pin_0, R2.Pin_0, R3.Pin_0
  N5: Componente1.D2, S2.Pin_3, S2.Pin_4, R3.Pin_1
  N6: Componente1.D3_PWM, S1.Pin_3, S1.Pin_4, R2.Pin_1
  N7: Componente1.5V, S1.Pin_1, S1.Pin_2, S2.Pin_1, S2.Pin_2
  N8: LED1.cathode, LED2.cathode, LED3.cathode, R1.Pin_1
