# Fritzing sketch id2502_MandoDistancia_0 (saved by Fritzing 0.8.3b)
breadboards: 1

parts:
  LCD1 = LCD screen
  RE1 = Rotary Encoder [package=THT]
  Parte2 = Arduino Uno (Rev3)
  IR1 = TSOP312.., 314.. [package=THT]

nets:
  N1: LCD1.VSS, LCD1.R/W, RE1.EncoderPinA
  N2: LCD1.VDD, RE1.EncoderPinC
  N3: LCD1.RS, Parte2.D7
  N4: LCD1.E, Parte2.D8
  N5: LCD1.DB4, Parte2.D9_PWM
  N6: LCD1.DB5, Parte2.D10_PWM/SS
  N7: LCD1.DB6, Parte2.ICSP_MOSI, Parte2.D11_PWM/MOSI
  N8: LCD1.DB7, Parte2.ICSP_MISO, Parte2.D12/MISO
  N9: RE1.EncoderPinB, IR1.GND, IR1.Vs
  N10: Parte2.D6_PWM, IR1.Data

notes:
  Receptor IR
  Control de brillo de display
  Display 16x2
  #include <LiquidCrystal.h>
  #include <IRremote.h>
  const int RECV_PIN = 6;
  IRrecv irrecv(RECV_PIN);
  decode_results results;
  String valor = "";
  LiquidCrystal lcd(7, 8, 9, 10, 11, 12);
  void setup() {
  lcd.begin(16, 2);
  lcd.setCursor(0, 0);
  lcd.print(" ");
  irrecv.enableIRIn();
  }
  void loop() {
  if (irrecv.decode(&results))
  {
  lcd.clear();
  switch (results.value) {case 16738455: valor="1"; break;case 16750695: valor="2"; break;case 16756815: valor="3"; break;case 16724175: valor="4"; break;case 16718055: valor="5"; break;case 16743045: valor="6"; break;case 16716015: valor="7"; break;case 16726215: valor="8"; break;case 16734885: valor="9"; break;case 16730805: valor="0"; break;case 16728765: valor="*"; break;case 16732845: valor="#"; break;case 16712445: valor="ok"; break;case 16736925: valor="sube"; break;case 16754775: valor="baja"; break;case 16720605: valor="izq"; break;case 16761405: valor="dch"; break;default:break;}
  lcd.begin(16, 2);
  lcd.setCursor(0, 0);
  lcd.print(valor);
  irrecv.resume();
  }
  delay(100);
  }
  CÓDIGOS GENERADOS POR EL MANDO
  1 16738455
  2 16750695
  3 16756815
  4 16724175
  5 16718055
  6 16743045
  7 16716015
  8 16726215
  9 16734885
  0 16730805
  * 16728765
  # 16732845
  ok 16712445
  sube 16736925
  baja 16754775
  izq 16720605
  dch 16761405
