# Fritzing sketch id2503_manual_servo_0 (saved by Fritzing 0.9.3b)
breadboards: 1

parts:
  Часть1 = Arduino Uno (Rev3)
  R1 = Rotary Potentiometer (Small) [maximum_resistance=100kΩ package=THT]
  J1 = Basic Servo

nets:
  N1: Часть1.A0, R1.wiper
  N2: Часть1.D8, J1.pulse
  5V: Часть1.5V, R1.leg2, J1.vcc
  GND: Часть1.GND, R1.leg1, J1.gnd

notes:
  У серво
  коричневый = -
  красный = +
  желтый = дата
