# Fritzing sketch id2504_ManuelTermometre_0 (saved by Fritzing 0.9.2b)
breadboards: 1

parts:
  T1 = LM35 Temperature Sensor [package="TO92 [THT]"]
  Part1 = Arduino Uno (Rev3)
  Grove1 = Grove 4 Digit Display
  J1 = Basic Servo
  LED1 = LED - 5mm [color="Red (633nm)" package="5 mm [THT]"]
  LED2 = LED - 5mm [color="Green (555nm)" package="5 mm [THT]"]

nets:
  VCC: T1.+Vs, Part1.5V, Grove1.VCC, J1.vcc
  N1: T1.Vout, Part1.A0
  GND: T1.GND, Part1.GND, Grove1.GND, J1.gnd, LED1.cathode, LED2.cathode
  N2: Part1.D8, J1.pulse
  N3: Part1.D12/MISO, Grove1.CLK
  N4: Part1.D13/SCK, Grove1.DIO
  N5: Part1.D2, LED2.anode
  N6: Part1.D3_PWM, LED1.anode
