# Fritzing sketch id2505_mapbagSchematic_0 (saved by Fritzing 0.9.0b)
breadboards: 1

parts:
  Part1 = Arduino Uno (Rev3)
  Part2 = LilyPad Buzzer
  Part3 = LilyPad Buzzer
  Part4 = LilyPad Buzzer
  Part5 = LilyPad Buzzer
  Part6 = LilyPad Buzzer
  Part7 = LilyPad Buzzer
  Part8 = LilyPad Buzzer
  Part9 = LilyPad Buzzer
  Part10 = Triple Axis Magnetometer - HMC5883 Breakout
  U1 = GP-2106 [package=gp-2106]
  Part11 = LilyPad LiPower

nets:
  N1: Part1.A4/SDA, Part10.SDA
  N2: Part1.A5/SCL, Part10.SCL
  N3: Part1.D8, Part9.+
  N4: Part1.D9_PWM, Part6.+
  N5: Part1.D10_PWM/SS, Part4.+
  N6: Part1.D11_PWM/MOSI, Part3.+
  N7: Part1.D12/MISO, Part2.+
  N8: Part1.D13/SCK, Part5.+
  N9: Part1.D2, U1.RX
  N10: Part1.D3_PWM, U1.TX
  N11: Part1.D6_PWM, Part7.+
  N12: Part1.D7, Part8.+
  GND: Part1.GND, Part2.-, Part3.-, Part4.-, Part6.-, Part7.-, Part8.-, Part9.-, Part10.GND, U1.GND, Part11.GND
  VCC: Part1.VIN, Part10.VCC, U1.VCC, Part11.+

notes:
  Each of the + of the lilyPad buzzers goes to a digital pin
  This isn't the compass I used but its just rx to digital 2 tx to digital 3
