# Fritzing sketch id2506_fps_enroll_0 (saved by Fritzing 0.8.5b)
breadboards: 1

parts:
  Componente1 = Arduino Uno (Rev3)
  R1 = Resistor [tolerance=±5% resistance=470 package=THT]  # not connected
  Componente2 = FTDI Basic Programmer
  R2 = Resistor [tolerance=±5% resistance=1k package=THT]

nets:
  GND: Componente1.GND, Componente2.GND, R2.Pin_0
  N1: Componente1.D4, R2.Pin_1
  N2: Componente1.D5_PWM, Componente2.RXI
  N3: Componente1.3V3, Componente2.POWER
