# Fritzing sketch id2507_mario_fitz_0 (saved by Fritzing 0.9.0b)
breadboards: 1

parts:
  Part1 = Arduino Uno (Rev3)
  R1 = Resistor [tolerance=±5% resistance=220 package=THT]
  J1 = Piezo Speaker
  LED1 = LED - 5mm [color="Red (633nm)" package="5 mm [THT]"]

nets:
  N1: Part1.D13/SCK, LED1.anode
  N2: Part1.D3_PWM, J1.pin2
  N3: Part1.3V3, R1.Pin_1
  N4: Part1.5V, J1.pin1
  N5: R1.Pin_0, LED1.cathode
