# Fritzing sketch id250_Leonardo_RFM69HCW_0 (saved by Fritzing 0.9.3b)
breadboards: 1

parts:
  Part1 = Arduino Leonardo (Rev3b)
  Part2 = adafruit [part_number="Adafruit #3070 and #3071"]

nets:
  N1: Part1.D2/SDA, Part2.connector22
  N2: Part1.D3_PWM/SCL, Part2.connector17
  N3: Part1.D4/A6, Part2.connector21
  N4: Part1.5V, Part2.connector14
  N5: Part1.GND, Part2.connector15
