# Fritzing sketch id2510_Untitled_Sketch_0 (saved by Fritzing 0.9.3b)
breadboards: 1

parts:
  Part1 = Arduino Uno (Rev3) - ICSP
  J1 = Piezo Speaker
  S1 = Momentary Switch [package=ksa_sealed_tac_switch]
  R1 = Resistor [tolerance=±5% resistance=10k package="0603 [SMD]"]
  LED1 = LED - 3mm [color="Red (633nm)" package="3 mm [THT]"]
  R2 = Resistor [tolerance=±5% resistance=100 package="0603 [SMD]"]

nets:
  N1: Part1.ICSP_MOSI, Part1.D11_PWM/MOSI, S1.1, R1.Pin_1
  N2: Part1.GND, J1.pin1, S1.3, R1.Pin_0, LED1.cathode
  N3: Part1.D10_PWM/SS, R2.Pin_1
  N4: Part1.D5_PWM, J1.pin2
  N5: LED1.anode, R2.Pin_0

notes:
  Ramazan BUĞDAYCI 2014010236041
  Bağlantı Şeması
