# Fritzing sketch id2511_schema_3x3_led_0 (saved by Fritzing 0.9.3b)
breadboards: 1

parts:
  Componente1 = Arduino Uno (Rev3)
  LED1 = LED - 5mm [color="Red (633nm)" package="5 mm [THT]"]
  LED2 = LED - 5mm [color="Red (633nm)" package="5 mm [THT]"]
  LED3 = LED - 5mm [color="Red (633nm)" package="5 mm [THT]"]
  LED4 = LED - 5mm [color="Red (633nm)" package="5 mm [THT]"]
  LED5 = LED - 5mm [color="Red (633nm)" package="5 mm [THT]"]
  LED6 = LED - 5mm [color="Red (633nm)" package="5 mm [THT]"]
  LED7 = LED - 5mm [color="Red (633nm)" package="5 mm [THT]"]
  LED8 = LED - 5mm [color="Red (633nm)" package="5 mm [THT]"]
  LED9 = LED - 5mm [color="Red (633nm)" package="5 mm [THT]"]
  R1 = Resistor [tolerance=±5% resistance=220 package=THT]
  R2 = Resistor [tolerance=±5% resistance=220 package=THT]
  R3 = Resistor [tolerance=±5% resistance=220 package=THT]
  Q1 = PNP-Transistor [package="TO92 [THT]"]
  Q2 = PNP-Transistor [package="TO92 [THT]"]
  Q3 = PNP-Transistor [package="TO92 [THT]"]
  R4 = Resistor [tolerance=±5% resistance=220 package=THT]
  R5 = Resistor [tolerance=±5% resistance=220 package=THT]
  R6 = Resistor [tolerance=±5% resistance=220 package=THT]

nets:
  N1: Componente1.D2, R1.Pin_0
  N2: Componente1.D3_PWM, R2.Pin_0
  N3: Componente1.D4, R3.Pin_0
  N4: Componente1.D5_PWM, R4.Pin_1
  N5: Componente1.D6_PWM, R5.Pin_1
  N6: Componente1.D7, R6.Pin_1
  N7: Componente1.GND, Q1.E, Q2.E, Q3.E
  N8: LED1.cathode, LED2.cathode, LED3.cathode, R1.Pin_1
  N9: LED1.anode, LED4.anode, LED7.anode, Q1.C
  N10: LED2.anode, LED5.anode, LED8.anode, Q2.C
  N11: LED3.anode, LED6.anode, LED9.anode, Q3.C
  N12: LED4.cathode, LED5.cathode, LED6.cathode, R2.Pin_1
  N13: LED7.cathode, LED8.cathode, LED9.cathode, R3.Pin_1
  N14: Q1.B, R4.Pin_0
  N15: Q2.B, R5.Pin_0
  N16: Q3.B, R6.Pin_0
