# Fritzing sketch id2512_2x2_0 (saved by Fritzing 0.8.7b)
breadboards: 1

parts:
  Parte1 = Arduino Uno (Rev3)
  LED1 = LED - 5mm [color="Red (633nm)" package="5 mm [THT]"]  # not connected
  LED2 = LED - 5mm [color="Red (633nm)" package="5 mm [THT]"]
  LED3 = LED - 5mm [color="Red (633nm)" package="5 mm [THT]"]
  LED4 = LED - 5mm [color="Red (633nm)" package="5 mm [THT]"]
  R1 = Resistor [tolerance=±5% resistance=220 package=THT]
  R2 = Resistor [tolerance=±5% resistance=220 package=THT]

nets:
  N1: Parte1.D10_PWM/SS, LED3.cathode
  N2: Parte1.D11_PWM/MOSI, LED2.cathode, LED4.cathode
  N3: Parte1.D5_PWM, R2.Pin_0
  N4: Parte1.D6_PWM, R1.Pin_1
  N5: LED3.anode, LED4.anode, R1.Pin_0
