# Fritzing sketch id2513_Projet_Mauv_v1_0 (saved by Fritzing 0.9.3b)
breadboards: 1

parts:
  Composant1 = Arduino Nano (Rev3.0)
  Composant2 = adafruit [part_number=VEML6070]
  OLED1 = 128x32_I2C_Monochrome_OLED_Display
  S1 = Momentary Switch [package=ksa_sealed_tac_switch]
  S2 = Momentary Switch [package=ksa_sealed_tac_switch]

nets:
  N1: Composant1.GND, Composant2.connector4, OLED1.connector4, S1.3, S1.4, S2.1, S2.2
  N2: Composant1.D6, S1.1, S1.2
  N3: Composant1.D9, S2.3, S2.4
  N4: Composant1.5V, Composant2.connector3, OLED1.connector6
  N5: Composant1.A5, Composant2.connector5
  N6: Composant1.A4, Composant2.connector6, OLED1.connector1
