# Fritzing sketch id2514_max7219_0 (saved by Fritzing 0.7.0b)
breadboards: 1

parts:
  MAX_7219 = MAX_7219
  100nF = Ceramic Capacitor [capacitance=100nF package="100 mil [THT, multilayer]"]
  VCC/GND = female pin header, 2 pins [form="♀ (female)"]
  LOAD/CLK = female pin header, 2 pins [form="♀ (female)"]
  DIN/DOUT = female pin header, 2 pins [form="♀ (female)"]
  7_SEG/ANODEN_0 = female pin header, 8 pins [form="♀ (female)"]
  0_DIG/KATHODEN_7 = female pin header, 8 pins [form="♀ (female)"]
  LOAD/CLK_2 = female pin header, 2 pins [form="♀ (female)"]
  ISET = Resistor [tolerance=±5% resistance=220 package=THT]
  10uF = Electrolytic Capacitor [capacitance=10µF package="100 mil [THT, electrolytic]"]

nets:
  N1: MAX_7219.connector0, DIN/DOUT.pin1
  N2: MAX_7219.connector1, 0_DIG/KATHODEN_7.pin8
  N3: MAX_7219.connector2, 0_DIG/KATHODEN_7.pin4
  N4: MAX_7219.connector3, MAX_7219.connector8, 100nF.1, VCC/GND.pin2, 10uF.-
  N5: MAX_7219.connector4, 0_DIG/KATHODEN_7.pin2
  N6: MAX_7219.connector5, 0_DIG/KATHODEN_7.pin6
  N7: MAX_7219.connector6, 0_DIG/KATHODEN_7.pin5
  N8: MAX_7219.connector7, 0_DIG/KATHODEN_7.pin1
  N9: MAX_7219.connector9, 0_DIG/KATHODEN_7.pin3
  N10: MAX_7219.connector10, 0_DIG/KATHODEN_7.pin7
  N11: MAX_7219.connector11, LOAD/CLK.pin1, LOAD/CLK_2.pin1
  N12: MAX_7219.connector12, LOAD/CLK.pin2, LOAD/CLK_2.pin2
  N13: MAX_7219.connector13, 7_SEG/ANODEN_0.pin2
  N14: MAX_7219.connector14, 7_SEG/ANODEN_0.pin7
  N15: MAX_7219.connector15, 7_SEG/ANODEN_0.pin3
  N16: MAX_7219.connector16, 7_SEG/ANODEN_0.pin8
  N17: MAX_7219.connector17, ISET.Pin_1
  N18: MAX_7219.connector18, 100nF.0, VCC/GND.pin1, ISET.Pin_0, 10uF.+
  N19: MAX_7219.connector19, 7_SEG/ANODEN_0.pin4
  N20: MAX_7219.connector20, 7_SEG/ANODEN_0.pin6
  N21: MAX_7219.connector21, 7_SEG/ANODEN_0.pin1
  N22: MAX_7219.connector22, 7_SEG/ANODEN_0.pin5
  N23: MAX_7219.connector23, DIN/DOUT.pin2
