# Fritzing sketch id2515_VR_pull_0 (saved by Fritzing 0.9.2b)
circuit board: 2.5cm x 1.2cm
breadboards: 1

parts:
  C3 = Ceramic Capacitor [capacitance=1µF voltage=50V package="1206 [SMD, multilayer]"]
  C4 = Ceramic Capacitor [capacitance=10nF voltage=50V package="1206 [SMD, multilayer]"]
  C2 = Ceramic Capacitor [capacitance=100nF voltage=50V package="1206 [SMD, multilayer]"]
  C1 = Ceramic Capacitor [capacitance=10nF voltage=50V package="1206 [SMD, multilayer]"]
  U1 = Unproven! [package=msop-10]
  R1 = Resistor [tolerance=±5% resistance=10k package="1206 [SMD]"]
  R2 = Resistor [tolerance=±5% resistance=10k package="1206 [SMD]"]
  R4 = Resistor [tolerance=±5% resistance=10k package="1206 [SMD]"]
  R5 = Resistor [tolerance=±5% resistance=10k package="1206 [SMD]"]

nets:
  N1: C3.0, C3.1, C4.0, C4.1, C2.0, C2.1, U1.STAT2, U1.VSS, U1.PROG, U1.VBAT, R4.Pin_1
  N2: C1.0, C1.1, U1.VDD, R1.Pin_0, R2.Pin_0
  N3: U1.~PG, R4.Pin_0
  N4: R2.Pin_1, R5.Pin_1

notes:
  VR+
  +5V
  OUT
  10k
  0,1u
  0,01u
  1u
  1n
  GND
  VR-
  1k
  5/12v
  Pullup
  TS
  PROTO
  Gul
  Grön
  Svart
  Blå
  Vit
  Röd
