# Fritzing sketch id2516_mjIno_0 (saved by Fritzing 0.8.3b)
circuit board: 1.99622cm x 2cm
breadboards: 1

parts:
  LED1 = smd LED [color="Blue (470nm)" package="1206 [SMD]"]
  C2 = Ceramic Capacitor [capacitance=100nF package="0805 [SMD, multilayer]"]
  C4 = Ceramic Capacitor [capacitance=100nF package="0805 [SMD, multilayer]"]
  R2 = Resistor [tolerance=±5% resistance=4.7k package="0805 [SMD]"]
  D1 = Rectifier Diode [part_number=1N4001 package="Melf DO-213 AB [SMD]"]
  C3 = Ceramic Capacitor [capacitance=100nF package="0805 [SMD, multilayer]"]
  IC1 = SO08 [chip_label=IC part_number=TDA7052A package=SO]
  R3 = Resistor [tolerance=±5% resistance=4.7k package="0805 [SMD]"]
  SPKR1 = Loudspeaker
  R4 = Resistor [tolerance=±5% resistance=470k package="0805 [SMD]"]
  J2 = male pin header, 2 pins [form="♂ (male)"]
  R1 = Resistor [tolerance=±5% resistance=220 package="0805 [SMD]"]
  C1 = Electrolytic Capacitor [capacitance=221µF voltage=50V package="200 mil [THT, electrolytic]"]
  J1 = female pin header, 3 pins [form="♀ (female)"]

nets:
  GND: LED1.cathode, C4.0, R2.Pin_0, IC1.3, IC1.6, R3.Pin_0, R4.Pin_1, J2.pin2, C1.-, J1.pin2
  N1: LED1.anode, R1.Pin_0
  N2: C2.0, C3.1, IC1.2
  N3: C2.1, R2.Pin_1, J1.pin1
  N4: C4.1, IC1.4, R4.Pin_0
  N5: D1.cathode, IC1.1, R1.Pin_1, C1.+
  N6: D1.anode, J2.pin1
  N7: C3.0, R3.Pin_1, J1.pin3
  N8: IC1.5, SPKR1.pin2
  N9: IC1.8, SPKR1.pin1

notes:
  mjIno Amplifier, Active Speaker for experiments and MP3 Player, _ C
  Powersupply from 5V to 15 V
  Connect here your earphone plug
  or your experiment.
  Right and left chanel are seperatet through C2 and C3.
  With R2 you can set the amplification. Range from cero ohm to 1 Megaohm.
  470 kOhm I've tested and it is good for MP3 or earphone connector.
  Speaker
  Power
  -
  +
  input
  hdf-mjf.de
  L
  R
  Optimized Fritzing Amplifier now called mjIno it is an Amplifier
  for Breadboard connect or your MP3-Players like cellphones.
  I always wonder when people contact an 8 ohm loudspeaker direct to the microcontroller pin.
  When we calculate the current through the speaker we get :
  I=U/R= 5V/8 ohm=0,625A=625 mA
  But microcontroller pin can only drive 20 mA to 40 mA!!!
  So I designed this little amplifier to solve this problem.
  Now you can connect your experiment by the mjIno and enjoying the sound.
  Have a lot of fun!
  Yours Michael J.
  Start your Order get PCB less 3 €
