# Fritzing sketch id2517_MayHew_Labs_MUX_Shield_0 (saved by Fritzing 0.7.0b)
breadboards: 3

parts:
  J8 = male pin header, 10 pins [form="♂ (male)"]
  J7 = male pin header, 8 pins [form="♂ (male)"]
  Power = male pin header, 8 pins [form="♂ (male)"]
  Analog_In = male pin header, 6 pins [form="♂ (male)"]
  I/O = female pin header, 24 pins [form="♀ (female)"]
  GND = female pin header, 24 pins [form="♀ (female)"]
  5V = female pin header, 24 pins [form="♀ (female)"]
  GND_2 = female pin header, 24 pins [form="♀ (female)"]
  5V_2 = female pin header, 24 pins [form="♀ (female)"]
  I/O_2 = female pin header, 24 pins [form="♀ (female)"]
  M0 = SSOP24 [chip_label=74HC4067 spacing=300mil package=SSOP]
  M1 = SSOP24 [chip_label=74HC4067 spacing=300mil package=SSOP]
  M2 = SSOP24 [chip_label=74HC4067 spacing=300mil package=SSOP]
  S1 = Pushbutton [package="[SMD]"]
  R1 = Resistor [tolerance=±5% resistance=1k package="0603 [SMD]"]
  LED1 = smd LED [color="Green (555nm)" package="0603 [SMD]"]
  LED2 = smd LED [color="Yellow (595nm)" package="0603 [SMD]"]
  R2 = Resistor [tolerance=±5% resistance=1k package="0603 [SMD]"]

nets:
  N1: J8.pin4, Power.pin6, Power.pin7, GND.pin1, GND.pin2, GND.pin3, GND.pin4, GND.pin5, GND.pin6, GND.pin7, GND.pin8, GND.pin9, GND.pin10, GND.pin11, GND.pin12, GND.pin13, GND.pin14, GND.pin15, GND.pin16, GND.pin17, GND.pin18, GND.pin19, GND.pin20, GND.pin21, GND.pin22, GND.pin23, GND.pin24, GND_2.pin1, GND_2.pin2, GND_2.pin3, GND_2.pin4, GND_2.pin5, GND_2.pin6, GND_2.pin7, GND_2.pin8, GND_2.pin9, GND_2.pin10, GND_2.pin11, GND_2.pin12, GND_2.pin13, GND_2.pin14, GND_2.pin15, GND_2.pin16, GND_2.pin17, GND_2.pin18, GND_2.pin19, GND_2.pin20, GND_2.pin21, GND_2.pin22, GND_2.pin23, GND_2.pin24, M0.12, M0.15, M1.12, M1.15, M2.12, M2.15, S1.Pin_1, S1.Pin_2, LED1.cathode, LED2.cathode
  N2: J8.pin5, R2.Pin_1
  N3: J7.pin2, M0.13, M1.13, M2.13
  N4: J7.pin3, M0.14, M1.14, M2.14
  N5: J7.pin4, M0.11, M1.11, M2.11
  N6: J7.pin5, M0.10, M1.10, M2.10
  N7: Power.pin3, S1.Pin_3, S1.Pin_4
  N8: Power.pin5, 5V.pin1, 5V.pin2, 5V.pin3, 5V.pin4, 5V.pin5, 5V.pin6, 5V.pin7, 5V.pin8, 5V.pin9, 5V.pin10, 5V.pin11, 5V.pin12, 5V.pin13, 5V.pin14, 5V.pin15, 5V.pin16, 5V.pin17, 5V.pin18, 5V.pin19, 5V.pin20, 5V.pin21, 5V.pin22, 5V.pin23, 5V.pin24, 5V_2.pin1, 5V_2.pin2, 5V_2.pin3, 5V_2.pin4, 5V_2.pin5, 5V_2.pin6, 5V_2.pin7, 5V_2.pin8, 5V_2.pin9, 5V_2.pin10, 5V_2.pin11, 5V_2.pin12, 5V_2.pin13, 5V_2.pin14, 5V_2.pin15, 5V_2.pin16, 5V_2.pin17, 5V_2.pin18, 5V_2.pin19, 5V_2.pin20, 5V_2.pin21, 5V_2.pin22, 5V_2.pin23, 5V_2.pin24, M0.24, M1.24, M2.24, R1.Pin_1
  N9: Analog_In.pin1, M0.1
  N10: Analog_In.pin2, M1.1
  N11: Analog_In.pin3, M2.1
  N12: I/O.pin1, M0.9
  N13: I/O.pin2, M0.8
  N14: I/O.pin3, M0.7
  N15: I/O.pin4, M0.6
  N16: I/O.pin5, M0.5
  N17: I/O.pin6, M0.4
  N18: I/O.pin7, M0.3
  N19: I/O.pin8, M0.2
  N20: I/O.pin9, M1.9
  N21: I/O.pin10, M1.8
  N22: I/O.pin11, M1.7
  N23: I/O.pin12, M1.6
  N24: I/O.pin13, M1.5
  N25: I/O.pin14, M1.4
  N26: I/O.pin15, M1.3
  N27: I/O.pin16, M1.2
  N28: I/O.pin17, M2.9
  N29: I/O.pin18, M2.8
  N30: I/O.pin19, M2.7
  N31: I/O.pin20, M2.6
  N32: I/O.pin21, M2.5
  N33: I/O.pin22, M2.4
  N34: I/O.pin23, M2.3
  N35: I/O.pin24, M2.2
  N36: I/O_2.pin1, M0.16
  N37: I/O_2.pin2, M0.17
  N38: I/O_2.pin3, M0.18
  N39: I/O_2.pin4, M0.19
  N40: I/O_2.pin5, M0.20
  N41: I/O_2.pin6, M0.21
  N42: I/O_2.pin7, M0.22
  N43: I/O_2.pin8, M0.23
  N44: I/O_2.pin9, M1.16
  N45: I/O_2.pin10, M1.17
  N46: I/O_2.pin11, M1.18
  N47: I/O_2.pin12, M1.19
  N48: I/O_2.pin13, M1.20
  N49: I/O_2.pin14, M1.21
  N50: I/O_2.pin15, M1.22
  N51: I/O_2.pin16, M1.23
  N52: I/O_2.pin17, M2.16
  N53: I/O_2.pin18, M2.17
  N54: I/O_2.pin19, M2.18
  N55: I/O_2.pin20, M2.19
  N56: I/O_2.pin21, M2.20
  N57: I/O_2.pin22, M2.21
  N58: I/O_2.pin23, M2.22
  N59: I/O_2.pin24, M2.23
  N60: R1.Pin_0, LED1.anode
  N61: LED2.anode, R2.Pin_0
