# Fritzing sketch id251_RGB_Sensor___TCS34725_0 (saved by Fritzing 0.9.3b)

parts:
  Part1 = adafruit [part_number="Adafruit #1334"]
  Part2 = Arduino Uno (Rev3)

nets:
  N1: Part1.connector8, Part2.5V
  N2: Part1.connector9, Part2.GND
  N3: Part1.connector11, Part2.A5/SCL
  N4: Part1.connector12, Part2.A4/SDA
