# Fritzing sketch id2520_mbd2pmd_0 (saved by Fritzing 0.7.12b)
breadboards: 1

parts:
  MICROSD = microSD Socket [package="Molex 502774-0891 [SMD]"]
  MBED = mbed
  Pad1 = Pad [width=4.18 height=0.76 connect=center]
  Pad2 = Pad [width=4.18 height=0.76 connect=center]
  Pad3 = Pad [width=4.18 height=0.76 connect=center]
  Pad4 = Pad [width=4.18 height=0.76 connect=center]
  Pad5 = Pad [width=4.18 height=0.76 connect=center]  # not connected
  Pad6 = Pad [width=4.18 height=0.76 connect=center]
  Pad7 = Pad [width=4.18 height=0.76 connect=center]  # not connected
  Pad8 = Pad [width=4.18 height=0.76 connect=center]  # not connected
  Pad9 = Pad [width=4.58 height=3.42 connect=center]
  Pad10 = Pad [width=4.58 height=3.42 connect=center]
  R1 = Resistor [tolerance=±5% resistance=3.3k package="0603 [SMD]"]
  R2 = Resistor [tolerance=±5% resistance=3.3k package="0603 [SMD]"]
  J2 = double row smd male pin header, 8 pins [form="♂ (male)"]
  U2 = SMD_QFN-28.fzp [chip_label=IC]
  J1 = double row female pin header, 12 pins [form="♀ (female)"]
  R3 = Resistor [tolerance=±5% resistance=3.3k package="0603 [SMD]"]
  R4 = Resistor [tolerance=±5% resistance=3.3k package="0603 [SMD]"]
  R5 = Resistor [tolerance=±5% resistance=3.3k package="0603 [SMD]"]
  R6 = Resistor [tolerance=±5% resistance=3.3k package="0603 [SMD]"]
  C1 = Ceramic Capacitor [capacitance=10µF package="0805 [SMD, multilayer]"]
  C2 = Ceramic Capacitor [capacitance=10µF package="0805 [SMD, multilayer]"]
  C3 = Ceramic Capacitor [capacitance=10µF package="0805 [SMD, multilayer]"]

nets:
  N1: MICROSD.CS, MBED.pin8
  N2: MICROSD.DI, MBED.pin5
  3.3V: MICROSD.VCC, MBED.VOUT, Pad4.pad, R1.Pin_0, R2.Pin_0, J2.pin4, J2.pin5, U2.connector25, J1.pin1, J1.pin12, C1.1, C2.1, C3.1
  N3: MICROSD.SCK, MBED.pin7
  GND: MICROSD.GND, MICROSD.SHIELD, MBED.GND, Pad9.pad, Pad10.pad, J2.pin3, J2.pin6, U2.connector0, U2.connector10, U2.connector22, U2.connector24, U2.connector27, J1.pin2, J1.pin11, C1.0, C2.0, C3.0
  N4: MICROSD.DO, MBED.pin6
  N5: MBED.nR, U2.connector21
  N6: MBED.pin9, U2.connector7
  N7: MBED.pin10, U2.connector8
  N8: MBED.pin11, U2.connector18, J1.pin8
  N9: MBED.pin12, U2.connector16, J1.pin9
  N10: MBED.pin13, U2.connector14, J1.pin10
  N11: MBED.pin14, U2.connector20, J1.pin7
  N12: MBED.pin15, R6.Pin_0
  N13: MBED.pin16, R5.Pin_0
  N14: MBED.pin17, R4.Pin_0
  N15: MBED.pin18, R3.Pin_0
  N16: MBED.pin21, U2.connector13, J1.pin3
  N17: MBED.pin22, U2.connector15, J1.pin4
  N18: MBED.pin23, U2.connector17, J1.pin5
  N19: MBED.pin24, U2.connector19, J1.pin6
  N20: MBED.pin25, U2.connector1
  N21: MBED.pin26, U2.connector2
  N22: MBED.pin27, R1.Pin_1, J2.pin1, J2.pin8, U2.connector3, U2.connector23
  N23: MBED.pin28, R2.Pin_1, J2.pin2, J2.pin7, U2.connector4, U2.connector26
  N24: MBED.pin29, U2.connector5
  N25: MBED.pin30, U2.connector6
  N26: MBED.TD+, Pad1.pad
  N27: MBED.TD-, Pad2.pad
  N28: MBED.RD+, Pad3.pad
  N29: MBED.RD-, Pad6.pad
  N30: U2.connector9, R5.Pin_1, R6.Pin_1
  N31: U2.connector12, R3.Pin_1, R4.Pin_1
