# Fritzing sketch id2521_Schematics_MC1_Gennaio_v5_0 (saved by Fritzing 0.9.1b)
breadboards: 2

parts:
  R3 = Rotary Potentiometer (Large) [maximum_resistance=100kΩ package=THT]
  R4 = Rotary Potentiometer (Large) [maximum_resistance=100kΩ package=THT]
  R5 = Rotary Potentiometer (Large) [maximum_resistance=100kΩ package=THT]
  LED1 = LED - 5mm [color="Red (633nm)" package="5 mm [THT]"]
  LED2 = LED - 5mm [color="Red (633nm)" package="5 mm [THT]"]
  LED3 = LED - 5mm [color="Red (633nm)" package="5 mm [THT]"]
  LED4 = LED - 5mm [color="Yellow (592nm)" package="5 mm [THT]"]
  LED5 = LED - 5mm [color="Green (555nm)" package="5 mm [THT]"]
  LED6 = LED - 5mm [color="Red (633nm)" package="5 mm [THT]"]
  LED7 = LED - 5mm [color="Green (555nm)" package="5 mm [THT]"]
  S1 = Square Pushbutton
  S2 = Square Pushbutton
  S3 = Square Pushbutton
  U5 = 2ChannelRelay
  S4 = Round Pushbutton
  S5 = Round Pushbutton
  M1 = Stepper Motor - Bipolar
  Part1 = Arduino Mega 2560 (Rev3)
  R6 = Resistor [tolerance=±5% resistance=220 package="1206 [SMD]"]
  R7 = Resistor [tolerance=±5% resistance=220 package="1206 [SMD]"]
  R8 = Resistor [tolerance=±5% resistance=220 package="1206 [SMD]"]
  R9 = Resistor [tolerance=±5% resistance=220 package="1206 [SMD]"]
  R10 = Resistor [tolerance=±5% resistance=220 package="1206 [SMD]"]
  R11 = Resistor [tolerance=±5% resistance=220 package="1206 [SMD]"]
  R12 = Resistor [tolerance=±5% resistance=220 package="1206 [SMD]"]

nets:
  N1: R3.leg1, R4.leg1, R5.leg1, Part1.5V
  N2: R3.wiper, Part1.A0
  N3: R3.leg2, R4.leg2, R5.leg2, LED1.cathode, LED2.cathode, LED3.cathode, LED4.cathode, LED5.cathode, LED6.cathode, LED7.cathode, S1.leg0, S2.leg0, S3.leg0, Part1.GND
  N4: R4.wiper, Part1.A2
  N5: R5.wiper, Part1.A1
  N6: LED1.anode, R11.Pin_0
  N7: LED2.anode, R12.Pin_1
  N8: LED3.anode, R10.Pin_1
  N9: LED4.anode, R9.Pin_1
  N10: LED5.anode, R8.Pin_1
  N11: LED6.anode, R7.Pin_0
  N12: LED7.anode, R6.Pin_0
  N13: S1.leg1, Part1.D28
  N14: S2.leg1, Part1.D24
  N15: S3.leg1, Part1.D26
  N16: U5.connector2, Part1.A3
  N17: U5.connector3, Part1.A4
  N18: U5.connector6, M1.C
  N19: U5.connector9, M1.D
  N20: S4.leg0, Part1.D34
  N21: S4.leg1, S5.leg1, Part1.D38
  N22: S5.leg0, Part1.D36
  N23: Part1.A5, R6.Pin_1
  N24: Part1.D12_PWM, R9.Pin_0
  N25: Part1.D11_PWM, R8.Pin_0
  N26: Part1.D10_PWM, R10.Pin_0
  N27: Part1.D9_PWM, R12.Pin_0
  N28: Part1.D8_PWM, R11.Pin_1
  N29: Part1.D22, R7.Pin_1

notes:
  Speed
  Acceleration
  Rotation
  Legenda
  R3 = R4 = R5 = 5K OHM
  EndStop Left
  EndStop Right
  USE L289H
  Motor Driver
  Board 1
  USE L289H
  Motor Driver
  Board 2
  USE Normal Open Contact
  StepDown 5.0 Volt Output
  Reset
  LED on top of the BOX
  LED in front of the box
  Central (not used)
  Left (not used)
  NOTE:
  Brown and Yellow are common and the pin is set to 0 (GND)
  Battery 12 V
  7.2 Ah
  Find the sketch at
  (MC1_Motor_Led_v7)
  https://codebender.cc/sketch:202740
