# Fritzing sketch id2522_mcp3008_0 (saved by Fritzing 0.9.2b)
breadboards: 1

parts:
  MCP1 = MCP3008 [part_number=gjhN]
  Raspberry_Pi1 = Raspberry Pi 2
  R1 = Rotary Potentiometer (Small) [maximum_resistance=100kΩ package=THT]
  R2 = Resistor [tolerance=±5% resistance=200 package="0402 [SMD]"]
  LED2 = smd LED [color="White (4500K)" package="0603 [SMD]"]

nets:
  N1: MCP1.connector0, R1.wiper
  N2: MCP1.connector8, MCP1.connector13, Raspberry_Pi1.GND, R1.leg1, LED2.cathode
  N3: MCP1.connector9, Raspberry_Pi1.GPIO8
  N4: MCP1.connector10, Raspberry_Pi1.GPIO10
  N5: MCP1.connector11, Raspberry_Pi1.GPIO9
  N6: MCP1.connector12, Raspberry_Pi1.GPIO11
  N7: MCP1.connector14, MCP1.connector15, Raspberry_Pi1.3v3, R1.leg2
  N8: Raspberry_Pi1.GPIO21, R2.Pin_1
  N9: R2.Pin_0, LED2.anode
