# Fritzing sketch id2523_mdb_dex_pcb_0 (saved by Fritzing 0.9.3b)
circuit board: 7.8257cm x 4.17844cm

parts:
  Atmega328p = atmega328 [package=dip]
  opt = TLP621 [package=THT]
  opt_2 = TLP621 [package=THT]
  C4 = Capacitor [package=cap-pth-small2]
  C5 = Capacitor [package=cap-pth-small2]
  180 = Resistor [tolerance=±5% resistance=220 package=THT]
  180_2 = Resistor [tolerance=±5% resistance=220 package=THT]
  180_3 = Resistor [tolerance=±5% resistance=220 package=THT]
  C9 = Capacitor Polarized [package=cpol-radial-10uf-25v]
  esp8266 = ESP8266_module [part_number=ESP8266]
  U1 = Voltage Regulator - 5V [package="TO220 [THT]"]
  XTAL2 = Crystal [frequency="16 Mhz" package=THT]
  C13 = Capacitor Polarized [package=cpol-radial-10uf-25v]
  180_4 = Resistor [tolerance=±5% resistance=220 package=THT]
  D2 = Diode [package=diode-1n4148]
  D3 = Diode [package=diode-1n4148]
  D4 = Diode [package=diode-1n4148]
  D5 = Diode [package=diode-1n4148]
  D6 = Diode [package=diode-1n4148]
  D7 = Diode [package=diode-1n4148]
  D8 = Diode [package=diode-1n4148]
  D9 = Diode [package=diode-1n4148]
  D10 = Diode [package=diode-1n4148]
  D11 = Diode [package=diode-1n4148]
  LED = LED - 3mm [color="Yellow (574nm)" package="3 mm [THT]"]
  -TH- = Temperature Sensor (Thermistor) [thermistor_type=NTC package=THT]
  -_+ = Piezo Speaker - PC Mount  [part_number=COM-07950]
  10k = Resistor [tolerance=±5% resistance=220 package=THT]
  J3 = double row female pin header, 10 pins [form="♀ (female)"]
  DEX = 3.5mm Audio Jack [package=audio-jack]
  Restock = SWITCH-MOMENTARY-2 [package=tactile-pth]

nets:
  N1: Atmega328p.D0_(RX), opt.Pin_4, 180_4.Pin_0
  N2: Atmega328p.D1_(TX), opt_2.Pin_2
  N3: Atmega328p.D2, Restock.2
  N4: Atmega328p.D3_(PWM), esp8266.connector0
  N5: Atmega328p.VCC, Atmega328p.AVCC, 180_3.Pin_0, C9.+, U1.output_voltage, 180_4.Pin_1, D10.A, -TH-.pin_0
  GND: Atmega328p.GND, opt.Pin_3, C4.2, C5.2, 180.Pin_1, C9.-, esp8266.connector6, U1.GND, C13.-, -_+.connector0, 10k.Pin_0, J3.pin5, J3.pin6, DEX.SLEEVE, Restock.1
  N6: Atmega328p.XLAT1, C5.1, XTAL2.pin_1
  N7: Atmega328p.XLAT2, C4.1, XTAL2.pin_0
  N8: Atmega328p.D7, LED.anode
  N9: Atmega328p.D8, esp8266.connector7
  N10: Atmega328p.D9_(PWM), DEX.LEFT
  N11: Atmega328p.D10_(PWM), DEX.RIGHT
  N12: Atmega328p.D11_(PWM), -_+.connector1
  N13: Atmega328p.A5, -TH-.pin_1, 10k.Pin_1
  N14: opt.Pin_1, 180_2.Pin_1
  N15: opt.Pin_2, opt_2.Pin_3, J3.pin4, J3.pin7
  N16: opt_2.Pin_1, 180_3.Pin_1
  N17: opt_2.Pin_4, J3.pin3, J3.pin8
  N18: 180.Pin_0, LED.cathode
  N19: 180_2.Pin_0, J3.pin2, J3.pin9
  N20: esp8266.connector1, esp8266.connector5, D11.C
  N21: U1.input_voltage, C13.+, D7.C
  N22: D2.A, J3.pin1, J3.pin10
  N23: D2.C, D3.A
  N24: D3.C, D4.A
  N25: D4.C, D5.A
  N26: D5.C, D6.A
  N27: D6.C, D8.A
  N28: D7.A, D9.C
  N29: D8.C, D9.A
  N30: D10.C, D11.A

notes:
  vendsystem.com
