# Fritzing sketch id2524_Me_Arm_V3.0_0 (saved by Fritzing 0.9.0b)
circuit board: 8.46667cm x 5.64444cm
breadboards: 1

parts:
  R1 = Rotary Potentiometer (Small) [maximum_resistance=100kΩ package=THT]
  R2 = Rotary Potentiometer (Small) [maximum_resistance=100kΩ package=THT]
  R3 = Rotary Potentiometer (Small) [maximum_resistance=100kΩ package=THT]
  R4 = Rotary Potentiometer (Small) [maximum_resistance=100kΩ package=THT]
  J1 = Basic Servo
  J2 = Basic Servo
  J3 = Basic Servo
  J4 = Basic Servo
  Composant1 = Arduino Uno (Rev3)

nets:
  VCC: R1.leg1, R2.leg1, R3.leg1, R4.leg1, J1.vcc, J2.vcc, J3.vcc, J4.vcc, Composant1.5V
  N1: R1.wiper, Composant1.A3
  GND: R1.leg2, R2.leg2, R3.leg2, R4.leg2, J1.gnd, J2.gnd, J3.gnd, J4.gnd, Composant1.GND
  N2: R2.wiper, Composant1.A2
  N3: R3.wiper, Composant1.A1
  N4: R4.wiper, Composant1.A0
  N5: J1.pulse, Composant1.D11_PWM/MOSI
  N6: J2.pulse, Composant1.D9_PWM
  N7: J3.pulse, Composant1.D10_PWM/SS
  N8: J4.pulse, Composant1.D6_PWM
