# Fritzing sketch id2525_ldr_enciende_leds_e_infrarrojos_0 (saved by Fritzing 0.9.0b)
breadboards: 1

parts:
  Parte1 = Arduino Uno (Rev3)
  R1 = Photocell (LDR) [package=THT]
  LED1 = smd LED [color="White (4500K)" package="0603 [SMD]"]
  LED2 = smd LED [color="Blue (525nm)" package="0603 [SMD]"]
  LED3 = smd LED [color="Green (570nm)" package="0603 [SMD]"]
  LED4 = smd LED [color="Yellow (595nm)" package="0603 [SMD]"]
  LED5 = smd LED [color="Red (633nm)" package="0603 [SMD]"]
  R2 = Resistor [tolerance=±5% resistance=220 package="1206 [SMD]"]
  R3 = Resistor [tolerance=±5% resistance=220 package="1206 [SMD]"]
  R4 = Resistor [tolerance=±5% resistance=220 package=THT]
  R5 = Resistor [tolerance=±5% resistance=220 package=THT]
  R6 = Resistor [tolerance=±5% resistance=220 package=THT]
  R7 = Resistor [tolerance=±5% resistance=10k package=THT]
  IR1 = TSOP312.., 314.. [package=THT]
  R8 = Resistor [tolerance=±5% resistance=220 package=THT]

nets:
  N1: Parte1.A0, R1.pin_0, R7.Pin_1
  N2: Parte1.D9_PWM, R4.Pin_0
  N3: Parte1.D11_PWM/MOSI, R3.Pin_0
  N4: Parte1.D12/MISO, R2.Pin_0
  N5: Parte1.GND, R1.pin_1, LED1.anode, LED2.anode, LED3.anode, LED4.anode, IR1.Vs
  N6: Parte1.D2, R8.Pin_0
  N7: Parte1.D5_PWM, R6.Pin_1
  N8: Parte1.D7, R5.Pin_0
  N9: Parte1.5V, R7.Pin_0, IR1.Data
  N10: LED1.cathode, R2.Pin_1
  N11: LED2.cathode, R3.Pin_1
  N12: LED3.cathode, R4.Pin_1
  N13: LED4.cathode, R5.Pin_1
  N14: LED5.cathode, R6.Pin_0
  N15: IR1.GND, R8.Pin_1
