# Fritzing sketch id2526_Current_Measurement_0 (saved by Fritzing 0.9.2b)
breadboards: 1

parts:
  Part1 = Arduino Uno (Rev3)
  R1 = Resistor [tolerance=±5% resistance=10 package=THT]
  U1 = NodeMCU
  U2 = LIPO-110mAh [package=lipo-110]

nets:
  N1: Part1.A1, R1.Pin_0, U1.connector15, U1.connector16, U2.+
  N2: Part1.GND, R1.Pin_1, U2.-
