# Fritzing sketch id2527_measurement_0 (saved by Fritzing 0.9.3b)
breadboards: 2

parts:
  Part1 = Bluetooth HC-05 Macho
  Part2 = Arduino Uno (Rev3)
  LCD1 = LCD screen
  R1 = Resistor [tolerance=±5% resistance=1k package=THT]
  R2 = Resistor [tolerance=±5% resistance=2.2k package=THT]
  R3 = Resistor [tolerance=±5% resistance=220 package=THT]
  U1 = POT_SWITCH [package=pot_pth]
  R5 = Resistor [tolerance=±5% resistance=1k package=THT]
  VCC1 = Battery block 9V
  R6 = Trimmer Potentiometer [maximum_resistance=10kΩ package=THT]
  IC1 = Voltage Regulator [package=to-220-alt]

nets:
  N1: Part1.TXD, Part2.D0/RX
  N2: Part1.RXD, R1.Pin_1, R2.Pin_0
  VCC: Part1.VCC, Part2.5V, LCD1.VDD, R6.leg2
  GND: Part1.GND, Part2.GND, LCD1.VSS, LCD1.R/W, LCD1.LED-, R2.Pin_1, U1.G$1_A, R5.Pin_1, R6.leg1
  N3: Part2.A5/SCL, U1.G$2_1, VCC1.-, IC1.IN
  N4: Part2.D11_PWM/MOSI, LCD1.E
  N5: Part2.D12/MISO, LCD1.RS
  N6: Part2.D1/TX, R1.Pin_0
  N7: Part2.D2, LCD1.DB4
  N8: Part2.D3_PWM, LCD1.DB5
  N9: Part2.D4, LCD1.DB6
  N10: Part2.D5_PWM, LCD1.DB7
  N11: LCD1.V0, R6.wiper
  N12: LCD1.LED+, R3.Pin_0
  N13: R5.Pin_0, IC1.OUT
  N14: VCC1.+, IC1.GND
