# Fritzing sketch id2528_StromSpannung_0 (saved by Fritzing 0.7.5b)
breadboards: 1

parts:
  Source = Screw terminal - 2 pins [package=THT]
  Load = Screw terminal - 2 pins [package=THT]
  Volt = Screw terminal - 2 pins [package=THT]
  Ampere = Screw terminal - 2 pins [package=THT]
  R31 = Rotary Potentiometer (Small) [maximum_resistance=10kΩ]
  R50 = Rotary Potentiometer (Small) [maximum_resistance=100kΩ]
  VCC1 = Battery block 9V
  IC10 = LM 358 Dual Op-Amp [package="SO 08 [SMD]"]
  IC30 = LM 358 Dual Op-Amp [package="SO 08 [SMD]"]
  D1 = Rectifier Diode [part_number=1N4001 package="Melf DO-213 AB [SMD]"]
  R41 = Resistor [tolerance=±5% resistance=2.2k package="0805 [SMD]"]
  R40 = Resistor [tolerance=±5% resistance=1k package="0805 [SMD]"]
  R22 = Resistor [tolerance=±5% resistance=100k package="0805 [SMD]"]
  C22 = Ceramic Capacitor [capacitance=100nF package="0805 [SMD, multilayer]"]
  C1 = Electrolytic Capacitor [capacitance=47µF voltage=50V package="1010 [SMD, electrolytic]"]
  R30 = Resistor [tolerance=±5% resistance=4.7 package="0805 [SMD]"]
  R21 = Resistor [tolerance=±5% resistance=100k package="0805 [SMD]"]
  C11 = Ceramic Capacitor [capacitance=100nF package="0805 [SMD, multilayer]"]
  C12 = Ceramic Capacitor [capacitance=100nF package="0805 [SMD, multilayer]"]
  R51 = Resistor [tolerance=±5% resistance=10k package="0805 [SMD]"]
  Rshunt = Resistor [tolerance=±5% resistance=1 package="1206 [SMD]"]
  R1 = Resistor [tolerance=±5% resistance=2.2k package="0805 [SMD]"]
  LED1 = smd LED [color="Red (633nm)" package="0805 [SMD]"]

nets:
  GND: Source.pin1, Volt.pin2, Ampere.pin2, IC10.connector0, IC10.connector1, IC30.connector2, IC30.connector4, C11.0, C12.1, Rshunt.Pin_1
  N1: Source.pin2, Load.pin1, IC10.connector4
  N2: Load.pin2, R30.Pin_1, Rshunt.Pin_0
  N3: Volt.pin1, IC10.connector5, IC10.connector6
  N4: Ampere.pin1, IC30.connector6, R41.Pin_0
  N5: R31.leg1, R31.wiper, IC30.connector0, R40.Pin_1
  N6: R31.leg2, IC30.connector1, R30.Pin_0, R51.Pin_0
  N7: R50.wiper, R51.Pin_1
  N8: R50.leg2, VCC1.-, IC10.connector3, IC30.connector3, R22.Pin_1, C22.0, C1.-, C12.0, LED1.cathode
  N9: VCC1.+, D1.anode
  N10: IC10.connector2, R22.Pin_0, C22.1, R21.Pin_1
  5V: IC10.connector7, IC30.connector7, D1.cathode, C1.+, R21.Pin_0, C11.1, R1.Pin_0
  N11: IC30.connector5, R41.Pin_1, R40.Pin_0
  N12: R1.Pin_1, LED1.anode

notes:
  VAUfA, Measuring voltage and current, _v04
  R31 is for calibrate the Current.
  Set it to 1 Volt per 1 mA.
  Here we need 30 V so we are able to measure
  +/- 0,01 v to 10 V
  and +/- 0,01 mA to 10 mA
  R50 is to eliminate error current. Set it to 0 V
  Voltage
  result 1 V / 1 V
  Ampere
  result 1 V / 1 mA
  Here is the connection
  for the load.
  Here ist the connection for the power source
  Here we are able to measure the power source very high impedant. Dependent on the OP we get up to 20 mega ohms.
  Depending on the unity gain you can measure
  1 V / 100 µA or in ouer case 1 V / 1 mA
