# Fritzing sketch id2529_meb_led_0 (saved by Fritzing 0.9.2b)
circuit board: 8.46667cm x 5.64444cm
breadboards: 1

parts:
  Widerstand = Resistor [tolerance=±5% resistance=220 package=THT]
  LED_(+_oben) = LED - 5mm [color="Red (633nm)" package="5 mm [THT]"]

nets:
  5V: Widerstand.Pin_0
  N1: Widerstand.Pin_1, LED_(+_oben).anode
  GND: LED_(+_oben).cathode
