# Fritzing sketch id252_Shield_para_Arduino_Nano_0 (saved by Fritzing 0.9.1b)
circuit board: 6.18002cm x 4.3271cm
breadboards: 1

parts:
  Componente1 = Arduino Nano (Rev3.0)
  J2 = female pin header, 15 pins [form="♀ (female)"]
  J4 = female pin header, 15 pins [form="♀ (female)"]
  J5 = female pin header, 15 pins [form="♀ (female)"]
  J6 = female pin header, 15 pins [form="♀ (female)"]
  J7 = female pin header, 15 pins [form="♀ (female)"]
  J8 = female pin header, 15 pins [form="♀ (female)"]
  Power_plug1 = Power plug
  D1 = Rectifier Diode [part_number=1N4001 package="300 mil [THT]"]
  J9 = female pin header, 4 pins [form="♀ (female)"]
  LED1 = LED - 5mm [color="Red (633nm)" package="5 mm [THT]"]
  R2 = Resistor [tolerance=±5% resistance=220 package=THT]

nets (from the pcb view):
  N1: Componente1.D1/TX, J8.pin15, J9.pin4
  N2: Componente1.D0/RX, J8.pin14, J9.pin3
  N3: Componente1.RESET, J2.pin13, J8.pin13
  GND: Componente1.GND, J2.pin14, J4.pin1, J4.pin2, J4.pin3, J4.pin4, J4.pin5, J4.pin6, J4.pin7, J4.pin8, J4.pin9, J4.pin10, J4.pin11, J4.pin12, J4.pin13, J4.pin14, J4.pin15, J5.pin1, J5.pin2, J5.pin3, J5.pin4, J5.pin5, J5.pin6, J5.pin7, J5.pin8, J5.pin9, J5.pin10, J5.pin11, J5.pin12, J5.pin13, J5.pin14, J5.pin15, J8.pin12, Power_plug1.GND, J9.pin2, R2.Pin_0
  N4: Componente1.D2, J8.pin11
  N5: Componente1.D3, J8.pin10
  N6: Componente1.D4, J8.pin9
  N7: Componente1.D5, J8.pin8
  N8: Componente1.D6, J8.pin7
  N9: Componente1.D7, J8.pin6
  N10: Componente1.D8, J8.pin5
  N11: Componente1.D9, J8.pin4
  N12: Componente1.D10, J8.pin3
  N13: Componente1.D11/MOSI, J8.pin2
  N14: Componente1.D12/MISO, J8.pin1
  N15: Componente1.VIN, J2.pin15, D1.anode
  N16: Componente1.5V, J2.pin12, J6.pin1, J6.pin2, J6.pin3, J6.pin4, J6.pin5, J6.pin6, J6.pin7, J6.pin8, J6.pin9, J6.pin10, J6.pin11, J6.pin12, J6.pin13, J6.pin14, J6.pin15, J7.pin1, J7.pin2, J7.pin3, J7.pin4, J7.pin5, J7.pin6, J7.pin7, J7.pin8, J7.pin9, J7.pin10, J7.pin11, J7.pin12, J7.pin13, J7.pin14, J7.pin15, J9.pin1, LED1.cathode
  N17: Componente1.A7, J2.pin11
  N18: Componente1.A6, J2.pin10
  N19: Componente1.A5, J2.pin9
  N20: Componente1.A4, J2.pin8
  N21: Componente1.A3, J2.pin7
  N22: Componente1.A2, J2.pin6
  N23: Componente1.A1, J2.pin5
  N24: Componente1.A0, J2.pin4
  N25: Componente1.AREF, J2.pin3
  N26: Componente1.3V3, J2.pin2
  N27: Componente1.D13/SCK, J2.pin1
  N28: Power_plug1.VCC, D1.cathode
  N29: LED1.anode, R2.Pin_1

notes:
  Desculpe-me, mas não tive paciência e organizar este esquemático
