# Fritzing sketch id2530_Schematic_Rough_Draft_0 (saved by Fritzing 0.9.2b)
breadboards: 1

parts:
  Part1 = Arduino Due (Rev2b)
  J1 = Basic Servo
  J2 = Basic Servo
  LCD1 = LCD screen
  R2 = Trimmer Potentiometer [maximum_resistance=10kΩ package=THT]
  V1 = DC Power [voltage=12V]
  V2 = DC Power [voltage=12V]
  Fuse1 = Fuse with Handler [part_number=Htc-15m]  # not connected
  Fuse2 = Fuse with Handler [part_number=Htc-15m]
  Hall_Effect = HALL-EFFECT [package=sc70]
  part = IC, DIP package, 6 pins [chip_label="Thermocouple Amplifier"]
  Flow_Meter = mystery part, 3 pins [chip_label=?]
  DC_Converter = IC, DIP package, 4 pins [chip_label="DC-DC Converter"]
  Part4 = Logic Level Converter
  R1 = RELAY [package=relay-g5q]
  R2_2 = RELAY [package=relay-g5q]
  R3 = RELAY [package=relay-g5q]
  R4 = RELAY [package=relay-g5q]  # not connected
  R5 = Resistor [tolerance=±5% resistance=220 package=THT]
  D1 = Rectifier Diode [part_number=1N4001 package="300 mil [THT]"]
  part_2 = IC, DIP package, 4 pins [chip_label=Contactor]
  part_3 = IC, DIP package, 6 pins [chip_label=ALLTRAX]
  R6 = Rotary Potentiometer (Small) [maximum_resistance=100kΩ package=THT]
  M1 = DC Motor
  GPS = IC, DIP package, 8 pins [chip_label=IC]
  U5 = MMA7361 [package=lga14]
  IC2 = IC, DIP package, 6 pins [chip_label="Thermocouple Amplifier"]
  IC4 = IC, DIP package, 6 pins [chip_label="Thermocouple Amplifier"]
  IC6 = IC, DIP package, 6 pins [chip_label="Thermocouple Amplifier"]
  F1 = FUSE [package=fuse_5mm]
  F2 = FUSE [package=fuse_5mm]
  U4 = mystery part, 6 pins [chip_label="frequency to voltage"]
  IC8 = IC, DIP package, 4 pins [chip_label=Contactor]
  D2 = Rectifier Diode [part_number=1N4001 package="300 mil [THT]"]  # not connected
  R7 = Resistor [tolerance=±5% resistance=220 package=THT]
  IC9 = IC, DIP package, 4 pins [chip_label=Alternator]  # not connected

nets:
  N1: Part1.A0, J1.pulse
  N2: Part1.A1, J2.pulse
  N3: Part1.A2, Part4.HV
  N4: Part1.A3, U5.XOUT
  N5: Part1.A4, U5.YOUT
  N6: Part1.A5, U5.ZOUT
  N7: Part1.IOREF, GPS.pin2, U5.VDD
  VCC: Part1.5V, J1.vcc, J2.vcc, LCD1.VDD, R2.leg1, Hall_Effect.VCC, part.pin1, Flow_Meter.pin1, IC2.pin1, IC4.pin1, IC6.pin1
  GND: Part1.GND, J1.gnd, J2.gnd, LCD1.VSS, LCD1.R/W, Hall_Effect.GND, part.pin3, Flow_Meter.pin3, GPS.pin1, U5.VSS, U4.pin2
  N8: Part1.VIN, DC_Converter.pin1
  N9: Part1.D11_PWM, LCD1.E
  N10: Part1.D12_PWM, LCD1.RS
  N11: Part1.D0/RX, part.pin6
  N12: Part1.D2_PWM, LCD1.DB6
  N13: Part1.D4_PWM/SS1, LCD1.DB5
  N14: Part1.D5_PWM, LCD1.DB4
  N15: Part1.D6_PWM, LCD1.DB7
  N16: Part1.D22, U5.GSELECT
  N17: Part1.D24, part.pin4
  N18: Part1.D25, part.pin5
  N19: Part1.D26, Flow_Meter.pin2
  N20: Part1.D27, GPS.pin3
  N21: Part1.D28, U5.0GD
  N22: LCD1.V0, R2.wiper
  N23: V1.V-, Fuse2.Connector1
  GND_2: V2.V-, R5.Pin_1, D1.anode, part_2.pin3, part_2.pin4, part_3.pin5, part_3.pin6, M1.pin_1
  N24: Fuse2.Connector2, F1.1, F2.2
  N25: Hall_Effect.OUT, U4.pin3
  N26: DC_Converter.pin4, F2.1
  N27: Part4.LV, R3.COIL1
  N28: R1.NO, part_2.pin1, F1.2
  N29: R2_2.NO, IC8.pin2
  N30: R5.Pin_0, D1.cathode, part_2.pin2, part_3.pin1
  N31: part_3.pin2, R6.leg2
  N32: part_3.pin3, R6.wiper
  N33: part_3.pin4, M1.pin_2
  N34: IC8.pin1, R7.Pin_0
  N35: IC8.pin4, R7.Pin_1
