# Fritzing sketch id2531_Mecanismo_0 (saved by Fritzing 0.9.3b)
breadboards: 1

parts:
  Componente1 = Arduino Uno (Rev3)
  R1 = Resistor [tolerance=±5% resistance=220 package=THT]
  R2 = Resistor [tolerance=±5% resistance=220 package=THT]
  LED1 = LED - 5mm [color="Red (633nm)" package="5 mm [THT]"]
  LED2 = LED - 5mm [color="Green (555nm)" package="5 mm [THT]"]
  LED3 = LED - 5mm [color="Blue (430nm)" package="5 mm [THT]"]
  R3 = Resistor [tolerance=±5% resistance=220 package="2512 [SMD]"]
  IC1 = H-Bridge [package=THT]
  M1 = DC Motor

nets:
  N1: Componente1.D8, IC1.1A
  N2: Componente1.D10_PWM/SS, IC1.2A
  N3: Componente1.D12/MISO, IC1.1_2EN
  GND: Componente1.GND, LED1.cathode, LED2.cathode, LED3.cathode, IC1.GND1, IC1.GND2, IC1.GND3, IC1.GND4
  N4: Componente1.D2, R2.Pin_1
  N5: Componente1.D4, R1.Pin_1
  N6: Componente1.D6_PWM, R3.Pin_1
  N7: Componente1.5V, IC1.VCC1
  N8: Componente1.VIN, IC1.VCC2
  N9: R1.Pin_0, LED2.anode
  N10: R2.Pin_0, LED1.anode
  N11: LED3.anode, R3.Pin_0
  N12: IC1.1Y, M1.pin_1
  N13: IC1.2Y, M1.pin_2
