# Fritzing sketch id2532_G15_Smart_Servo_Chain_w%3AArduino_0 (saved by Fritzing 0.9.2b)
breadboards: 1

parts:
  Part1 = Arduino Mega 2560 (Rev3)
  R1 = Resistor [tolerance=±0.5% resistance=22k package="0402 [SMD]"]
  R1_2 = Resistor [tolerance=±0.5% resistance=1M package="0402 [SMD]"]
  R2 = Resistor [tolerance=±5% resistance=220 package=THT]
  J1 = Basic Servo

nets:
  5V: Part1.5V, R1.Pin_1, R1_2.Pin_1, J1.vcc
  GND: Part1.GND, J1.gnd
  N1: Part1.D44, R2.Pin_1
  N2: R1.Pin_0, R1_2.Pin_0, R2.Pin_0, J1.pulse

notes:
  5V to + On Breadboard
  GRD to - On Breadboard
  Digital Pin 44 to Breadboard
  22k Resistor placed directly from + 5V Power to new row on Breadboard
  From the 22K Pull-Up Resistor Row, to row 45 on breadboard
  (To booste the power of the signal coming from arduino comm line going to the servo chain)
  5V to Servo Chain Directly
  Ground to Servo Chain Directly
  22k Resistor
  5V Power
  Ground
  Data to servo chain (From Pin 44)
  SMART SERVO CHAIN1
  1K Resistor
