# Fritzing sketch id2536_Medidor_de_Fluxo_0 (saved by Fritzing 0.9.3b)
breadboards: 1

parts:
  Componente1 = MicroSD Card Module
  Componente2 = Arduino Uno (Rev3)
  LCD1 = LCD screen
  U1 = DS1307 [package=so08]

nets:
  GND: Componente1.GND, LCD1.VSS, LCD1.R/W, LCD1.LED-, U1.GND
  VCC: Componente1.VCC, U1.VCC
  N1: Componente1.MISO, Componente2.D12/MISO
  N2: Componente1.MOSI, Componente2.D11_PWM/MOSI
  N3: Componente1.SCK, Componente2.D13/SCK
  N4: Componente1.CS, Componente2.D10_PWM/SS
  N5: Componente2.A0, LCD1.DB4
  N6: Componente2.A1, LCD1.DB5
  N7: Componente2.A2, LCD1.DB6
  N8: Componente2.A3, LCD1.DB7
  N9: Componente2.A4/SDA, U1.SDA
  N10: Componente2.A5/SCL, U1.SCL
  N11: Componente2.D8, LCD1.E
  N12: Componente2.D7, LCD1.RS
  N13: LCD1.VDD, LCD1.LED+

notes:
  Display LCD -
  Vss, RW e K - GND
  Vdd, A - 5V
  RS - 5
  RW - 7
  E - 8
  D4 - A0
  D5 - A1
  D6 - A2
  D7 - A3
  SD
  GND - GND
  5V - 5V
  CS - 10
  MOSI - 11
  SCK - 13
  MISO - 12
  Realtime Clock
  GND - GND
  VCC - 5V
  SDA - A4
  SCL - A5
  Preto Amarelo Vermelho
  Sensor de Fluxo
  preto - gnd
  vermelho - 5V
  amarelo - 2
