# Fritzing sketch id2537_DisplayTemperatura_0 (saved by Fritzing 0.8.3b)
breadboards: 1

parts:
  LCD1 = LCD screen
  RHT1 = Humidity and Temperature Sensor RHT03
  RE1 = Rotary Encoder [package=THT]
  Parte1 = Humidity Sensor - HIH-4030 Breakout
  Parte2 = Arduino Uno (Rev3)

nets:
  VSS: LCD1.VSS, LCD1.R/W, RHT1.GND_2, RE1.EncoderPinA, Parte1.GND
  N1: LCD1.VDD, RE1.EncoderPinC
  N2: LCD1.RS, Parte2.D7
  N3: LCD1.E, Parte2.D8
  N4: LCD1.DB4, Parte2.D9_PWM
  N5: LCD1.DB5, Parte2.D10_PWM/SS
  N6: LCD1.DB6, Parte2.ICSP_MOSI, Parte2.D11_PWM/MOSI
  N7: LCD1.DB7, Parte2.ICSP_MISO, Parte2.D12/MISO
  N8: RHT1.Data-signal, RE1.EncoderPinB, Parte1.OUT
  N9: RHT1.GND_1, Parte2.D3_PWM
  N10: Parte1.VCC, Parte2.A0

notes:
  Sensor de lluvia
  Sensor temperatura y humedad
  Control de brillo de display
  Display 16x2
  #include <LiquidCrystal.h>
  #include "DHT.h"
  #define DHTPIN 3
  #define DHTTYPE DHT11
  DHT dht(DHTPIN, DHTTYPE);
  LiquidCrystal lcd(7, 8, 9, 10, 11, 12);
  void setup() {
  dht.begin(); //Se inicia el sensor
  }
  void loop() {
  float h = dht.readHumidity();
  float t = dht.readTemperature();
  lcd.begin(16, 2);
  lcd.setCursor(0, 0);
  lcd.print("Temp");
  lcd.setCursor(0, 1);
  lcd.print("Humedad");
  lcd.setCursor(9, 0);
  lcd.print(t);
  lcd.print(" C");
  lcd.setCursor(9, 1);
  lcd.print(h);
  lcd.print(" %");
  delay(2000);
  if (analogRead(A0)!=0) {lcd.clear(); lcd.print("Llueve "); lcd.print(analogRead(A0)); delay(5000);}
  }
