# Fritzing sketch id253_Ada's_Intuition_0 (saved by Fritzing 0.9.3b)

parts:
  R1 = BBC MICROBIT
  R2 = Resistor [tolerance=±5% resistance=100 package=THT]
  R3 = Resistor [tolerance=±5% resistance=100 package=THT]
  R4 = Resistor [tolerance=±5% resistance=100 package=THT]
  LED1 = RGB LED (com. cathode, rbg) [package="5 mm [THT]"]

nets:
  N1: R1.connector1, LED1.common_cathode
  N2: R1.connector12, R3.Pin_0
  N3: R1.connector18, R4.Pin_0
  N4: R1.connector23, R2.Pin_0
  N5: R2.Pin_1, LED1.green_anode
  N6: R3.Pin_1, LED1.blue_anode
  N7: R4.Pin_1, LED1.red_anode
