# Fritzing sketch id2541_MEGA_BREAD_LCD_0 (saved by Fritzing 0.9.3b)
breadboards: 4

parts:
  R2_C3 = Pushbutton [package="[SMD]"]
  R2_C4 = Pushbutton [package="[SMD]"]
  R2_C6 = Pushbutton [package="[SMD]"]
  R3_C2 = Pushbutton [package="[SMD]"]
  R3_C10 = Pushbutton [package="[SMD]"]
  R2_C1 = Pushbutton [package="[SMD]"]
  R1_C9 = Pushbutton [package="[SMD]"]
  R2_C7 = Pushbutton [package="[SMD]"]
  R2_C10 = Pushbutton [package="[SMD]"]
  R1_C1 = Pushbutton [package="[SMD]"]
  R3_C7 = Pushbutton [package="[SMD]"]
  R1_C5 = Pushbutton [package="[SMD]"]
  R2_C8 = Pushbutton [package="[SMD]"]
  R3_C5 = Pushbutton [package="[SMD]"]
  R3_C3 = Pushbutton [package="[SMD]"]
  R1_C10 = Pushbutton [package="[SMD]"]
  R1_C4 = Pushbutton [package="[SMD]"]
  R3_C4 = Pushbutton [package="[SMD]"]
  R1_C2 = Pushbutton [package="[SMD]"]
  R1_C3 = Pushbutton [package="[SMD]"]
  R3_C8 = Pushbutton [package="[SMD]"]
  R2_C5 = Pushbutton [package="[SMD]"]
  R1_C6 = Pushbutton [package="[SMD]"]
  R2_C2 = Pushbutton [package="[SMD]"]
  R2_C9 = Pushbutton [package="[SMD]"]
  R1_C8 = Pushbutton [package="[SMD]"]
  R3_C9 = Pushbutton [package="[SMD]"]
  R3_C6 = Pushbutton [package="[SMD]"]
  R1_C1_2 = Pushbutton [package="[SMD]"]
  R1_C7 = Pushbutton [package="[SMD]"]
  Part1 = Arduino Mega 2560 (Rev3)
  VCC1 = Battery block 9V
  LED1 = LED - 5mm [color="Red (633nm)" package="5 mm [THT]"]
  R4 = Resistor [tolerance=±5% resistance=220 package=THT]
  R5 = Resistor [tolerance=±5% resistance=220 package=THT]
  R6 = Resistor [tolerance=±5% resistance=220 package=THT]
  R7 = Resistor [tolerance=±5% resistance=220 package=THT]
  R8 = Resistor [tolerance=±5% resistance=220 package=THT]
  R9 = Resistor [tolerance=±5% resistance=220 package=THT]
  R10 = Resistor [tolerance=±5% resistance=220 package=THT]
  R11 = Resistor [tolerance=±5% resistance=220 package=THT]
  R12 = Resistor [tolerance=±5% resistance=220 package=THT]
  R13 = Resistor [tolerance=±5% resistance=220 package=THT]
  R14 = Resistor [tolerance=±5% resistance=220 package=THT]
  R15 = Rotary Potentiometer (Small) [maximum_resistance=100kΩ package=THT]
  R16 = Rotary Potentiometer (Small) [maximum_resistance=100kΩ package=THT]
  LCD1 = LCD screen

nets (from the breadboard view):
  N1: R2_C3.Pin_1, R2_C3.Pin_2, R3_C3.Pin_1, R3_C3.Pin_2, R1_C1_2.Pin_1, R1_C1_2.Pin_2, R7.Pin_0
  N2: R2_C3.Pin_3, R2_C3.Pin_4, R2_C4.Pin_3, R2_C4.Pin_4, R2_C6.Pin_3, R2_C6.Pin_4, R2_C1.Pin_3, R2_C1.Pin_4, R2_C7.Pin_3, R2_C7.Pin_4, R2_C10.Pin_3, R2_C10.Pin_4, R2_C8.Pin_3, R2_C8.Pin_4, R2_C5.Pin_3, R2_C5.Pin_4, R2_C2.Pin_3, R2_C2.Pin_4, R2_C9.Pin_3, R2_C9.Pin_4, Part1.D53
  N3: R2_C4.Pin_1, R2_C4.Pin_2, R1_C4.Pin_1, R1_C4.Pin_2, R3_C4.Pin_1, R3_C4.Pin_2, R8.Pin_0
  N4: R2_C6.Pin_1, R2_C6.Pin_2, R1_C6.Pin_1, R1_C6.Pin_2, R3_C6.Pin_1, R3_C6.Pin_2, R10.Pin_0
  N5: R3_C2.Pin_1, R3_C2.Pin_2, R1_C2.Pin_1, R1_C2.Pin_2, R2_C2.Pin_1, R2_C2.Pin_2, R6.Pin_0
  N6: R3_C2.Pin_3, R3_C2.Pin_4, R3_C10.Pin_3, R3_C10.Pin_4, R3_C7.Pin_3, R3_C7.Pin_4, R3_C5.Pin_3, R3_C5.Pin_4, R3_C3.Pin_3, R3_C3.Pin_4, R3_C4.Pin_3, R3_C4.Pin_4, R1_C3.Pin_3, R1_C3.Pin_4, R3_C8.Pin_3, R3_C8.Pin_4, R3_C9.Pin_3, R3_C9.Pin_4, R3_C6.Pin_3, R3_C6.Pin_4, Part1.D51
  N7: R3_C10.Pin_1, R3_C10.Pin_2, R2_C10.Pin_1, R2_C10.Pin_2, R1_C10.Pin_1, R1_C10.Pin_2, R14.Pin_0
  N8: R2_C1.Pin_1, R2_C1.Pin_2, R1_C1.Pin_1, R1_C1.Pin_2, R1_C3.Pin_1, R1_C3.Pin_2, R5.Pin_0
  N9: R1_C9.Pin_1, R1_C9.Pin_2, R2_C9.Pin_1, R2_C9.Pin_2, R3_C9.Pin_1, R3_C9.Pin_2, R13.Pin_0
  N10: R1_C9.Pin_3, R1_C9.Pin_4, R1_C1.Pin_3, R1_C1.Pin_4, R1_C5.Pin_3, R1_C5.Pin_4, R1_C10.Pin_3, R1_C10.Pin_4, R1_C4.Pin_3, R1_C4.Pin_4, R1_C2.Pin_3, R1_C2.Pin_4, R1_C6.Pin_3, R1_C6.Pin_4, R1_C8.Pin_3, R1_C8.Pin_4, R1_C1_2.Pin_3, R1_C1_2.Pin_4, R1_C7.Pin_3, R1_C7.Pin_4, Part1.D52
  N11: R2_C7.Pin_1, R2_C7.Pin_2, R3_C7.Pin_1, R3_C7.Pin_2, R1_C7.Pin_1, R1_C7.Pin_2, R11.Pin_0
  N12: R1_C5.Pin_1, R1_C5.Pin_2, R3_C5.Pin_1, R3_C5.Pin_2, R2_C5.Pin_1, R2_C5.Pin_2, R9.Pin_0
  N13: R2_C8.Pin_1, R2_C8.Pin_2, R3_C8.Pin_1, R3_C8.Pin_2, R1_C8.Pin_1, R1_C8.Pin_2, R12.Pin_0
  N14: Part1.A8, R13.Pin_1
  N15: Part1.A1, R6.Pin_1
  N16: Part1.A2, R7.Pin_1
  N17: Part1.A3, R8.Pin_1
  N18: Part1.A4, R9.Pin_1
  N19: Part1.A5, R10.Pin_1
  N20: Part1.A6, R11.Pin_1
  N21: Part1.D13_PWM, LED1.anode
  5V: Part1.5V, R15.leg2, R16.leg2, LCD1.VDD
  GND: Part1.GND, VCC1.-, R4.Pin_0, R15.leg1, R16.leg1, LCD1.VSS, LCD1.R/W, LCD1.LED-
  N22: Part1.VIN, VCC1.+
  N23: Part1.D28, LCD1.RS
  N24: Part1.D29, LCD1.E
  N25: Part1.D30, LCD1.DB0
  N26: Part1.D31, LCD1.DB1
  N27: Part1.D32, LCD1.DB2
  N28: Part1.D33, LCD1.DB3
  N29: Part1.D34, LCD1.DB4
  N30: Part1.D35, LCD1.DB5
  N31: Part1.D36, LCD1.DB6
  N32: Part1.D37, LCD1.DB7
  N33: LED1.cathode, R4.Pin_1
  N34: R15.wiper, LCD1.LED+
  N35: R16.wiper, LCD1.V0
