# Fritzing sketch id2543_MEGA_BREAD_HANK_THE_HEXABOT_0 (saved by Fritzing 0.9.3b)
breadboards: 12

parts:
  Part2 = Arduino Mega 2560 (Rev3)
  U3 = RELAY-SOLIDSTATE [package=relay-s108t02]
  U4 = RELAY-SOLIDSTATE [part_number="Right Power" package=relay-s108t02]
  J19 = Basic Servo [part_number=FRB]
  J20 = Basic Servo [part_number=FRC]
  J21 = Basic Servo [part_number=BLC]
  J22 = Basic Servo [part_number=FLC]
  J23 = Basic Servo [part_number=MLC]
  J24 = Basic Servo [part_number=BLB]
  J25 = Basic Servo [part_number=FLB]
  J26 = Basic Servo [part_number=MLB]
  J27 = Basic Servo [part_number=MRC]
  J28 = Basic Servo [part_number=BRC]
  J29 = Basic Servo [part_number=MRB]
  J30 = Basic Servo [part_number=BRB]
  J31 = Basic Servo [part_number=BLA]
  J32 = Basic Servo [part_number=MLA]
  J33 = Basic Servo [part_number=BRA]
  J34 = Basic Servo [part_number=MRA]
  J35 = Basic Servo [part_number=FLA]
  J36 = Basic Servo [part_number=FRA]
  Power_plug1 = Power plug
  R1 = Resistor [tolerance=±5% resistance=220 package=THT]
  R2 = Resistor [tolerance=±5% resistance=220 package=THT]
  LED1 = LED - 5mm [color="Red (633nm)" package="5 mm [THT]"]
  LED2 = LED - 5mm [color="Red (633nm)" package="5 mm [THT]"]
  hc-sr2 = hc-sr04 [part_number=Distance]

nets (from the breadboard view):
  GND: Part2.GND, U3.-, U4.-, J19.gnd, J20.gnd, J21.gnd, J22.gnd, J23.gnd, J24.gnd, J25.gnd, J26.gnd, J27.gnd, J28.gnd, J29.gnd, J30.gnd, J31.gnd, J32.gnd, J33.gnd, J34.gnd, J35.gnd, J36.gnd, Power_plug1.GND, R1.Pin_1, R2.Pin_1, hc-sr2.GND
  VCC: Part2.5V, U3.T1, U4.T1, Power_plug1.VCC, hc-sr2.VCC
  N1: Part2.D2_PWM, hc-sr2.Echo
  N2: Part2.D3_PWM, hc-sr2.Trig
  N3: Part2.D5_PWM, U3.+, LED2.anode
  N4: Part2.D7_PWM, U4.+, LED1.anode
  N5: Part2.D23, J35.pulse
  N6: Part2.D24, J22.pulse
  N7: Part2.D26, J26.pulse
  N8: Part2.D27, J32.pulse
  N9: Part2.D28, J23.pulse
  N10: Part2.D30, J24.pulse
  N11: Part2.D31, J31.pulse
  N12: Part2.D32, J21.pulse
  N13: Part2.D42, J28.pulse
  N14: Part2.D44, J30.pulse
  N15: Part2.D45, J33.pulse
  N16: Part2.D46, J27.pulse
  N17: Part2.D48, J29.pulse
  N18: Part2.D49, J34.pulse
  N19: Part2.D50, J20.pulse
  N20: Part2.D52, J19.pulse
  N21: Part2.D53, J36.pulse
  VCC_2: U3.T2, J21.vcc, J22.vcc, J23.vcc, J24.vcc, J25.vcc, J26.vcc, J31.vcc, J32.vcc, J35.vcc
  VCC_3: U4.T2, J19.vcc, J20.vcc, J27.vcc, J28.vcc, J29.vcc, J30.vcc, J33.vcc, J34.vcc, J36.vcc
  N22: R1.Pin_0, LED1.cathode
  N23: R2.Pin_0, LED2.cathode

notes:
  The Diode is very important.
  5 Volt power relay's
  Left and Right servo's
  Power supply:
  5.7 Volt Tablet LiOn
