# Fritzing sketch id2544_MEGA_BREAD___Hello_World_0 (saved by Fritzing 0.9.3b)
breadboards: 4

parts:
  S1 = Pushbutton [package="[THT]"]
  Part1 = Arduino Mega 2560 (Rev3)
  VCC1 = Battery
  LCD1 = LCD screen
  R2 = Resistor [tolerance=±5% resistance=220 package=THT]

nets (from the breadboard view):
  GND: S1.Pin_1, S1.Pin_2, Part1.GND, VCC1.-, LCD1.VSS, LCD1.R/W, R2.Pin_1
  N1: S1.Pin_3, S1.Pin_4, Part1.RESET
  N2: Part1.D21/SCL, Part1.SCL
  N3: Part1.D20/SDA, Part1.SDA
  N4: Part1.D12_PWM, LCD1.RS
  N5: Part1.D11_PWM, LCD1.E
  N6: Part1.D10_PWM, LCD1.LED+
  N7: Part1.D9_PWM, LCD1.V0
  5V: Part1.5V, VCC1.+, LCD1.VDD
  N8: Part1.D2_PWM, LCD1.DB7
  N9: Part1.D3_PWM, LCD1.DB6
  N10: Part1.D4_PWM, LCD1.DB5
  N11: Part1.D5_PWM, LCD1.DB4
  N12: LCD1.LED-, R2.Pin_0
