# Fritzing sketch id2545_MEGA_BREAD_KEYBOARD_0 (saved by Fritzing 0.9.3b)
breadboards: 1

parts:
  R2_C3 = Pushbutton [package="[SMD]"]
  R2_C4 = Pushbutton [package="[SMD]"]
  R2_C6 = Pushbutton [package="[SMD]"]
  R3_C2 = Pushbutton [package="[SMD]"]
  R3_C10 = Pushbutton [package="[SMD]"]
  R2_C1 = Pushbutton [package="[SMD]"]
  R1_C9 = Pushbutton [package="[SMD]"]
  R2_C7 = Pushbutton [package="[SMD]"]
  R2_C10 = Pushbutton [package="[SMD]"]
  R1_C1 = Pushbutton [package="[SMD]"]
  R3_C7 = Pushbutton [package="[SMD]"]
  R1_C5 = Pushbutton [package="[SMD]"]
  R2_C8 = Pushbutton [package="[SMD]"]
  R3_C5 = Pushbutton [package="[SMD]"]
  R3_C3 = Pushbutton [package="[SMD]"]
  R1_C10 = Pushbutton [package="[SMD]"]
  R1_C4 = Pushbutton [package="[SMD]"]
  R3_C4 = Pushbutton [package="[SMD]"]
  R1_C2 = Pushbutton [package="[SMD]"]
  R1_C3 = Pushbutton [package="[SMD]"]
  R3_C8 = Pushbutton [package="[SMD]"]
  R2_C5 = Pushbutton [package="[SMD]"]
  R1_C6 = Pushbutton [package="[SMD]"]
  R2_C2 = Pushbutton [package="[SMD]"]
  R2_C9 = Pushbutton [package="[SMD]"]
  R1_C8 = Pushbutton [package="[SMD]"]
  R3_C9 = Pushbutton [package="[SMD]"]
  R3_C6 = Pushbutton [package="[SMD]"]
  R1_C1_2 = Pushbutton [package="[SMD]"]
  R1_C7 = Pushbutton [package="[SMD]"]
  Part1 = Arduino Mega 2560 (Rev3)
  VCC1 = Battery block 9V
  R1 = Resistor [tolerance=±5% resistance=220 package=THT]
  R2 = Resistor [tolerance=±5% resistance=220 package=THT]
  R3 = Resistor [tolerance=±5% resistance=220 package=THT]
  LED1 = LED - 5mm [color="Red (633nm)" package="5 mm [THT]"]
  R4 = Resistor [tolerance=±5% resistance=220 package=THT]

nets (from the schematic view):
  N1: R2_C3.Pin_1, R2_C3.Pin_2, R3_C3.Pin_3, R3_C3.Pin_4, R1_C3.Pin_3, R1_C3.Pin_4, Part1.A2
  N2: R2_C3.Pin_3, R2_C3.Pin_4, R2_C4.Pin_3, R2_C4.Pin_4, R2_C6.Pin_3, R2_C6.Pin_4, R2_C1.Pin_3, R2_C1.Pin_4, R2_C7.Pin_3, R2_C7.Pin_4, R2_C10.Pin_3, R2_C10.Pin_4, R2_C8.Pin_3, R2_C8.Pin_4, R2_C5.Pin_3, R2_C5.Pin_4, R2_C2.Pin_3, R2_C2.Pin_4, R2_C9.Pin_3, R2_C9.Pin_4, R1.Pin_0
  N3: R2_C4.Pin_1, R2_C4.Pin_2, R1_C4.Pin_3, R1_C4.Pin_4, R3_C4.Pin_3, R3_C4.Pin_4, Part1.A3
  N4: R2_C6.Pin_1, R2_C6.Pin_2, R1_C6.Pin_3, R1_C6.Pin_4, R3_C6.Pin_3, R3_C6.Pin_4, Part1.A5
  N5: R3_C2.Pin_1, R3_C2.Pin_2, R3_C10.Pin_1, R3_C10.Pin_2, R3_C7.Pin_1, R3_C7.Pin_2, R3_C5.Pin_1, R3_C5.Pin_2, R3_C3.Pin_1, R3_C3.Pin_2, R3_C4.Pin_1, R3_C4.Pin_2, R3_C8.Pin_1, R3_C8.Pin_2, R3_C9.Pin_1, R3_C9.Pin_2, R3_C6.Pin_1, R3_C6.Pin_2, R1_C1_2.Pin_1, R1_C1_2.Pin_2, R2.Pin_0
  N6: R3_C2.Pin_3, R3_C2.Pin_4, R1_C2.Pin_3, R1_C2.Pin_4, R2_C2.Pin_1, R2_C2.Pin_2, Part1.A1
  N7: R3_C10.Pin_3, R3_C10.Pin_4, R2_C10.Pin_1, R2_C10.Pin_2, R1_C10.Pin_3, R1_C10.Pin_4, Part1.A9
  N8: R2_C1.Pin_1, R2_C1.Pin_2, R1_C1.Pin_3, R1_C1.Pin_4, R1_C1_2.Pin_3, R1_C1_2.Pin_4, Part1.A0
  N9: R1_C9.Pin_1, R1_C9.Pin_2, R1_C1.Pin_1, R1_C1.Pin_2, R1_C5.Pin_1, R1_C5.Pin_2, R1_C10.Pin_1, R1_C10.Pin_2, R1_C4.Pin_1, R1_C4.Pin_2, R1_C2.Pin_1, R1_C2.Pin_2, R1_C3.Pin_1, R1_C3.Pin_2, R1_C6.Pin_1, R1_C6.Pin_2, R1_C8.Pin_1, R1_C8.Pin_2, R1_C7.Pin_1, R1_C7.Pin_2, R3.Pin_0
  N10: R1_C9.Pin_3, R1_C9.Pin_4, R2_C9.Pin_1, R2_C9.Pin_2, R3_C9.Pin_3, R3_C9.Pin_4, Part1.A8
  N11: R2_C7.Pin_1, R2_C7.Pin_2, R3_C7.Pin_3, R3_C7.Pin_4, R1_C7.Pin_3, R1_C7.Pin_4, Part1.A6
  N12: R1_C5.Pin_3, R1_C5.Pin_4, R3_C5.Pin_3, R3_C5.Pin_4, R2_C5.Pin_1, R2_C5.Pin_2, Part1.A4
  N13: R2_C8.Pin_1, R2_C8.Pin_2, R3_C8.Pin_3, R3_C8.Pin_4, R1_C8.Pin_3, R1_C8.Pin_4, Part1.A7
  N14: Part1.D13_PWM, LED1.anode
  N15: Part1.GND, VCC1.-, R4.Pin_0
  N16: Part1.VIN, VCC1.+
  N17: Part1.D38, R3.Pin_1
  N18: Part1.D39, R1.Pin_1
  N19: LED1.cathode, R4.Pin_1
