# Fritzing sketch id2546_CUTSIE_WHUN_NPN_H_BRIDGE_0 (saved by Fritzing 0.9.3b)
breadboards: 1

parts:
  Q1 = NPN-Transistor [package="TO92 [THT]"]
  Q2 = NPN-Transistor [package="TO92 [THT]"]
  Q3 = NPN-Transistor [package="TO92 [THT]"]
  Q4 = NPN-Transistor [package="TO92 [THT]"]
  R1 = Resistor [tolerance=±5% resistance=100k package=THT]
  R2 = Resistor [tolerance=±5% resistance=100k package=THT]
  R3 = Resistor [tolerance=±5% resistance=100k package=THT]
  R4 = Resistor [tolerance=±5% resistance=100k package=THT]
  M1 = DC Motor [part_number="Modified Servo"]
  VCC1 = 2x 18650 battery
  U1 = Voltage Regulator - 5V [package="DPak [SMD]"]
  C1 = Electrolytic Capacitor [capacitance=10nF package="100 mil [THT, electrolytic]"]
  C2 = Electrolytic Capacitor [capacitance=100nF package="100 mil [THT, electrolytic]"]
  S1 = Pushbutton [package="[THT]"]
  S2 = Pushbutton [package="[THT]"]
  R5 = Resistor [tolerance=±5% resistance=220 package=THT]
  R6 = Resistor [tolerance=±5% resistance=220 package=THT]
  LED1 = LED - 5mm [color="Red (633nm)" package="5 mm [THT]"]
  LED2 = LED - 5mm [color="Red (633nm)" package="5 mm [THT]"]

nets:
  N1: Q1.E, Q2.C, M1.pin_2
  N2: Q1.B, R1.Pin_1
  N3: Q1.C, Q4.C, VCC1.connector1, U1.input_voltage, C2.+
  N4: Q2.E, Q3.E, VCC1.connector0, U1.GND, C1.-, C2.-, R5.Pin_0, R6.Pin_0
  N5: Q2.B, R3.Pin_1
  N6: Q3.B, R2.Pin_0
  N7: Q3.C, Q4.E, M1.pin_1
  N8: Q4.B, R4.Pin_0
  N9: R1.Pin_0, R2.Pin_1, S1.Pin_1, S1.Pin_2, LED1.cathode
  N10: R3.Pin_0, R4.Pin_1, S2.Pin_1, S2.Pin_2, LED2.cathode
  N11: U1.output_voltage, C1.+, S1.Pin_3, S1.Pin_4, S2.Pin_3, S2.Pin_4
  N12: R5.Pin_1, LED2.anode
  N13: R6.Pin_1, LED1.anode

notes:
  7.4 Volt Supply
  5.0 Volt Buss
  Forward / Backward
  Triggers are both PWM Compatible. LED's and triggers use 5V Supply
  Forward / Backward
  H-Bridges use the full 7.4V Supply
