# Fritzing sketch id2548_MegaRC_0 (saved by Fritzing 0.9.3b)
circuit board: 8.46667cm x 5.64444cm
breadboards: 1

parts:
  Componente1 = Arduino Mega 2560 (Rev3)
  J2 = Basic Servo
  J4 = Basic Servo
  J1 = Basic Servo
  Battery = adafruit [part_number=2011]
  J3 = Basic Servo
  J6 = male pin header, 5 pins [form="♂ (male)"]
  J7 = male pin header, 2 pins [form="♂ (male)"]

nets (from the schematic view):
  N1: Componente1.D12_PWM, J6.pin1
  N2: Componente1.D11_PWM, J6.pin2
  N3: Componente1.D10_PWM, J6.pin3
  N4: Componente1.D9_PWM, J6.pin4
  N5: Componente1.D8_PWM, J6.pin5
  N6: Componente1.IOREF, J7.pin1
  GND: Componente1.GND, J4.gnd, J1.gnd, J7.pin2
  N7: Componente1.D2_PWM, J1.pulse
  N8: Componente1.D3_PWM, J2.pulse
  N9: Componente1.D4_PWM, J3.pulse
  N10: Componente1.D5_PWM, J4.pulse
  GND_2: J2.gnd, Battery.connector2, J3.gnd
  VCC: J2.vcc, J4.vcc, J1.vcc, Battery.connector1, J3.vcc

notes:
  [7.4 V LIPO reduced to 5V]
  To receiver channels
  receiver power
