# Fritzing sketch id2549_Mega_Motor_Shield_v01revB_0 (saved by Fritzing 0.6.3b)
breadboards: 2

parts:
  PWR1 = LM2676
  Vin = Power plug
  C1 = Electrolytic Capacitor [capacitance=15µF voltage=50V package="100 mil [THT, electrolytic]"]
  C2 = Electrolytic Capacitor [capacitance=15µF voltage=50V package="100 mil [THT, electrolytic]"]
  C3 = Ceramic Capacitor [capacitance=0.47µF voltage=50V package="0805 [SMD, multilayer]"]
  C4 = Ceramic Capacitor [capacitance=0.01µF voltage=10V package="0805 [SMD, multilayer]"]
  C5 = Electrolytic Capacitor [capacitance=180µF voltage=16V package="100 mil [THT, electrolytic]"]
  Ain = female pin header, 8 pins [form="♀ (female)"]
  J1 = screw terminal, 8 pins
  Driver_1 = A3988S
  C7 = Ceramic Capacitor [capacitance=100nF voltage=50V package="0805 [SMD, multilayer]"]
  C6 = Ceramic Capacitor [capacitance=100nF voltage=50V package="0805 [SMD, multilayer]"]
  Bluetooth = female pin header, 6 pins [form="♂ (male)"]
  R1 = Resistor [tolerance=±1% resistance=0.4 power=0.25W package="0805 [SMD]"]
  R2 = Resistor [tolerance=±1% resistance=0.4 package="0805 [SMD]"]
  R3 = Resistor [tolerance=±1% resistance=0.4 package="0805 [SMD]"]
  R4 = Resistor [tolerance=±1% resistance=0.4 package="0805 [SMD]"]
  R6 = Resistor [tolerance=±5% resistance=16.6k power=0.25W package="0805 [SMD]"]
  J5 = screw terminal, 8 pins
  Driver_2 = A3988S
  C8 = Ceramic Capacitor [capacitance=100nF voltage=50V package="0805 [SMD, multilayer]"]
  C9 = Ceramic Capacitor [capacitance=100nF voltage=50V package="0805 [SMD, multilayer]"]
  R9 = Resistor [tolerance=±1% resistance=0.4 power=0.25W package="0805 [SMD]"]
  R10 = Resistor [tolerance=±1% resistance=0.4 package="0805 [SMD]"]
  R11 = Resistor [tolerance=±1% resistance=0.4 package="0805 [SMD]"]
  R12 = Resistor [tolerance=±1% resistance=0.4 package="0805 [SMD]"]
  R13 = Resistor [tolerance=±5% resistance=5k power=0.25W package="0805 [SMD]"]
  R14 = Resistor [tolerance=±5% resistance=16.6k power=0.25W package="0805 [SMD]"]
  R15 = Resistor [tolerance=±5% resistance=5k power=0.25W package="0805 [SMD]"]
  C10 = Ceramic Capacitor [capacitance=100nF voltage=50V package="0805 [SMD, multilayer]"]
  Mega_Motor_Shield = Arduino Mega
  S = female pin header, 12 pins [form="♂ (male)"]
  +5 = female pin header, 12 pins [form="♂ (male)"]
  G = female pin header, 12 pins [form="♂ (male)"]
  D2 = Schottky_Diode [part_number=1N5817]
  L1 = Inductor [part_number=SPD127R]
  Vin_2 = female pin header, 2 pins [form="♂ (male)"]

nets (from the pcb view):
  N1: PWR1.connector0, C4.0, D2.connector0, L1.connector0
  N2: PWR1.connector1, Vin.VCC, C1.+, C2.+, C3.0, Driver_1.connector4, Driver_1.connector22, C7.0, Driver_2.connector4, Driver_2.connector22, C8.0, Vin_2.pin1
  N3: PWR1.connector2, C4.1
  GND: PWR1.connector3, Vin.GND, C1.-, C2.-, C3.1, C5.-, Driver_1.connector15, Driver_1.connector29, Bluetooth.pin1, Bluetooth.pin2, R1.Pin_1, R2.Pin_1, R3.Pin_1, R4.Pin_1, Driver_2.connector15, Driver_2.connector29, R9.Pin_1, R10.Pin_1, R11.Pin_1, R12.Pin_1, R13.Pin_1, R15.Pin_1, C10.1, Mega_Motor_Shield.GND, G.pin1, G.pin2, G.pin3, G.pin4, G.pin5, G.pin6, G.pin7, G.pin8, G.pin9, G.pin10, G.pin11, G.pin12, D2.connector1
  N4: PWR1.connector5, C5.+, Driver_1.connector10, Bluetooth.pin3, R6.Pin_0, Driver_2.connector10, R14.Pin_0, C10.0, Mega_Motor_Shield.+5V, +5.pin1, +5.pin2, +5.pin3, +5.pin4, +5.pin5, +5.pin6, +5.pin7, +5.pin8, +5.pin9, +5.pin10, +5.pin11, +5.pin12, L1.connector1
  N5: Ain.pin1, Mega_Motor_Shield.A0
  N6: Ain.pin2, Mega_Motor_Shield.A1
  N7: Ain.pin3, Mega_Motor_Shield.A2
  N8: Ain.pin4, Mega_Motor_Shield.A3
  N9: Ain.pin5, Mega_Motor_Shield.A4
  N10: Ain.pin6, Mega_Motor_Shield.A5
  N11: Ain.pin7, Mega_Motor_Shield.A6
  N12: Ain.pin8, Mega_Motor_Shield.A7
  N13: J1.pin1, Driver_1.connector25
  N14: J1.pin2, Driver_1.connector23
  N15: J1.pin3, Driver_1.connector21
  N16: J1.pin4, Driver_1.connector19
  N17: J1.pin5, Driver_1.connector7
  N18: J1.pin6, Driver_1.connector5
  N19: J1.pin7, Driver_1.connector3
  N20: J1.pin8, Driver_1.connector1
  N21: Driver_1.connector0, Mega_Motor_Shield.D31
  N22: Driver_1.connector2, R1.Pin_0
  N23: Driver_1.connector6, R2.Pin_0
  N24: Driver_1.connector8, Mega_Motor_Shield.D2
  N25: Driver_1.connector9, Mega_Motor_Shield.D3
  N26: Driver_1.connector11, Driver_1.connector12, Driver_1.connector13, Driver_1.connector14, R6.Pin_1, R13.Pin_0
  N27: Driver_1.connector16, Mega_Motor_Shield.D4
  N28: Driver_1.connector17, Mega_Motor_Shield.D5
  N29: Driver_1.connector18, Mega_Motor_Shield.D36
  N30: Driver_1.connector20, R4.Pin_0
  N31: Driver_1.connector24, R3.Pin_0
  N32: Driver_1.connector26, Mega_Motor_Shield.D37
  N33: Driver_1.connector27, Mega_Motor_Shield.D34
  N34: Driver_1.connector28, Mega_Motor_Shield.D35
  N35: Driver_1.connector30, C7.1
  N36: Driver_1.connector31, C6.1
  N37: Driver_1.connector32, C6.0
  N38: Driver_1.connector33, Mega_Motor_Shield.D32
  N39: Driver_1.connector34, Mega_Motor_Shield.D33
  N40: Driver_1.connector35, Mega_Motor_Shield.D30
  N41: Bluetooth.pin4, Mega_Motor_Shield.D0RX
  N42: Bluetooth.pin5, Mega_Motor_Shield.D1TX
  N43: J5.pin1, Driver_2.connector25
  N44: J5.pin2, Driver_2.connector23
  N45: J5.pin3, Driver_2.connector21
  N46: J5.pin4, Driver_2.connector19
  N47: J5.pin5, Driver_2.connector7
  N48: J5.pin6, Driver_2.connector5
  N49: J5.pin7, Driver_2.connector3
  N50: J5.pin8, Driver_2.connector1
  N51: Driver_2.connector0, Mega_Motor_Shield.D23
  N52: Driver_2.connector2, R9.Pin_0
  N53: Driver_2.connector6, R12.Pin_0
  N54: Driver_2.connector8, Mega_Motor_Shield.D6
  N55: Driver_2.connector9, Mega_Motor_Shield.D7
  N56: Driver_2.connector11, Driver_2.connector12, Driver_2.connector13, Driver_2.connector14, R14.Pin_1, R15.Pin_0
  N57: Driver_2.connector16, Mega_Motor_Shield.D8
  N58: Driver_2.connector17, Mega_Motor_Shield.D9
  N59: Driver_2.connector18, Mega_Motor_Shield.D28
  N60: Driver_2.connector20, R11.Pin_0
  N61: Driver_2.connector24, R10.Pin_0
  N62: Driver_2.connector26, Mega_Motor_Shield.D29
  N63: Driver_2.connector27, Mega_Motor_Shield.D26
  N64: Driver_2.connector28, Mega_Motor_Shield.D27
  N65: Driver_2.connector30, C8.1
  N66: Driver_2.connector31, C9.1
  N67: Driver_2.connector32, C9.0
  N68: Driver_2.connector33, Mega_Motor_Shield.D24
  N69: Driver_2.connector34, Mega_Motor_Shield.D25
  N70: Driver_2.connector35, Mega_Motor_Shield.D22
  N71: Mega_Motor_Shield.VIN, Vin_2.pin2
  N72: Mega_Motor_Shield.D42, S.pin1
  N73: Mega_Motor_Shield.D43, S.pin2
  N74: Mega_Motor_Shield.D44, S.pin3
  N75: Mega_Motor_Shield.D45, S.pin4
  N76: Mega_Motor_Shield.D46, S.pin5
  N77: Mega_Motor_Shield.D47, S.pin6
  N78: Mega_Motor_Shield.D48, S.pin7
  N79: Mega_Motor_Shield.D49, S.pin8
  N80: Mega_Motor_Shield.D50, S.pin9
  N81: Mega_Motor_Shield.D51, S.pin10
  N82: Mega_Motor_Shield.D52, S.pin11
  N83: Mega_Motor_Shield.D53, S.pin12

notes:
  REV 2
  2011/11/30
  enable
