# Fritzing sketch id254_tv_b_gone_atmega328p_0 (saved by Fritzing 0.8.7b)
circuit board: 5.13474cm x 2.86852cm
breadboards: 1

parts:
  XTAL1 = Crystal [frequency="16 Mhz" package=THT]
  Q1 = NPN-Transistor [package="TO92 [THT]"]
  R1_(47ohm) = Resistor [tolerance=±5% resistance=47 package=THT]
  IR_LED = LED - 5mm [color="Infrared (880nm)" package="5 mm [THT]"]
  R2 = Resistor [tolerance=±5% resistance=10 package=THT]
  S1 = Pushbutton [package="[THT]"]
  VCC1 = Battery
  LED = LED - 3mm [color="Green (565nm)" package="3 mm [THT]"]
  Atmega328p = atmega328 [package=dip]

nets:
  N1: XTAL1.pin_0, Atmega328p.XLAT1
  N2: XTAL1.pin_1, Atmega328p.XLAT2
  GND: Q1.E, S1.Pin_3, S1.Pin_4, VCC1.-, LED.cathode, Atmega328p.GND, Atmega328p.D5_(PWM)
  N3: Q1.B, R1_(47ohm).Pin_1
  N4: Q1.C, R2.Pin_0
  N5: R1_(47ohm).Pin_0, Atmega328p.D3_(PWM)
  N6: IR_LED.cathode, R2.Pin_1
  N7: IR_LED.anode, VCC1.+, Atmega328p.VCC, Atmega328p.AVCC
  N8: S1.Pin_1, S1.Pin_2, Atmega328p.D2
  N9: LED.anode, Atmega328p.D7

notes:
  TV-B-Gone
  TV-B-Gone para Arduino según esquema y especipicaciones encontradas en: http://www.righto.com/2010/11/improved-arduino-tv-b-gone.html
  El pin 5 va a tierra para usar los código europeos.
