# Fritzing sketch id2550_RelayBoard_for_StigChristian_0 (saved by Fritzing 0.8.5b)
breadboards: 3

parts:
  U1 = 74HC595 [package="DIP16 [THT]"]
  U2 = atmega328 [package=dip]
  HEF1 = HEF4094 [package="DIP16 [THT]"]  # not connected
  C1 = Electrolytic Capacitor [capacitance=10µF voltage=35V package="100 mil [THT, electrolytic]"]
  JP1 = Header 2 [package=screwterminal-3.5mm-2_lock]
  K5 = Relay [part_number=FRS1B-S package=THT]
  K6 = Relay [part_number=FRS1B-S package=THT]
  K1 = Relay [part_number=FRS1B-S package=THT]
  K7 = Relay [part_number=FRS1B-S package=THT]
  K8 = Relay [part_number=FRS1B-S package=THT]
  OI-O_8 = TLP621 [package=THT]
  OI-O_6 = TLP621 [package=THT]
  OI-O_7 = TLP621 [package=THT]
  R1 = RPACK* [package=rpack-sip-pth-5]
  R2 = RPACK* [package=rpack-sip-pth-5]
  OI-O_3 = TLP621 [package=THT]
  OI-O_4 = TLP621 [package=THT]
  OI-O_5 = TLP621 [package=THT]
  OI-O_2 = TLP621 [package=THT]
  OI-O_1 = TLP621 [package=THT]
  Q1 = NPN-Transistor [package="TO92 [THT]"]
  Q2 = NPN-Transistor [package="TO92 [THT]"]
  Q3 = NPN-Transistor [package="TO92 [THT]"]
  Q4 = NPN-Transistor [package="TO92 [THT]"]
  Q5 = NPN-Transistor [package="TO92 [THT]"]
  Q6 = NPN-Transistor [package="TO92 [THT]"]
  Q7 = NPN-Transistor [package="TO92 [THT]"]
  Q8 = NPN-Transistor [package="TO92 [THT]"]
  R3 = Resistor [tolerance=±5% resistance=220 package=THT]
  R4 = Resistor [tolerance=±5% resistance=220 package=THT]
  R5 = Resistor [tolerance=±5% resistance=220 package=THT]
  R6 = Resistor [tolerance=±5% resistance=220 package=THT]
  R7 = Resistor [tolerance=±5% resistance=220 package=THT]
  R8 = Resistor [tolerance=±5% resistance=220 package=THT]
  R9 = Resistor [tolerance=±5% resistance=220 package=THT]
  R10 = Resistor [tolerance=±5% resistance=220 package=THT]
  D1 = Rectifier Diode [part_number=1N4001 package="300 mil [THT]"]
  D2 = Rectifier Diode [part_number=1N4001 package="300 mil [THT]"]
  D3 = Rectifier Diode [part_number=1N4001 package="300 mil [THT]"]
  D4 = Rectifier Diode [part_number=1N4001 package="300 mil [THT]"]
  D5 = Rectifier Diode [part_number=1N4001 package="300 mil [THT]"]
  D6 = Rectifier Diode [part_number=1N4001 package="300 mil [THT]"]
  D7 = Rectifier Diode [part_number=1N4001 package="300 mil [THT]"]
  D8 = Rectifier Diode [part_number=1N4001 package="300 mil [THT]"]
  K4 = Relay [part_number=FRS1B-S package=THT]
  K3 = Relay [part_number=FRS1B-S package=THT]
  J8 = screw terminal, 3 pins
  J7 = screw terminal, 3 pins
  J6 = screw terminal, 3 pins
  J4 = screw terminal, 3 pins
  J2 = screw terminal, 3 pins
  J1 = screw terminal, 3 pins
  J5 = screw terminal, 3 pins
  J3 = screw terminal, 3 pins
  K2 = Relay [part_number=FRS1B-S package=THT]
  U3 = Voltage Regulator - 5V [package="TO220 [THT]"]

nets:
  N1: U1.Q1, OI-O_2.Pin_1
  N2: U1.Q2, OI-O_3.Pin_1
  N3: U1.Q3, OI-O_4.Pin_1
  N4: U1.Q4, OI-O_5.Pin_1
  N5: U1.Q5, OI-O_6.Pin_1
  N6: U1.Q6, OI-O_7.Pin_1
  N7: U1.Q7, OI-O_8.Pin_1
  N8: U1.GND, U2.GND#7, JP1.1, R1.1, R2.1, Q1.E, Q2.E, Q3.E, Q4.E, Q5.E, Q6.E, Q7.E, Q8.E
  N9: U1.Q0, OI-O_1.Pin_1
  +5v: U1.VCC, U2.VCC, U3.output_voltage
  N10: C1.-, U3.GND
  +12v: C1.+, JP1.2, K5.COIL1, K6.COIL1, K1.COIL1, K7.COIL1, K8.COIL1, R3.Pin_0, R4.Pin_0, R5.Pin_0, R6.Pin_0, R7.Pin_0, R8.Pin_0, R9.Pin_0, R10.Pin_0, D1.cathode, D2.cathode, D3.cathode, D4.cathode, D5.cathode, D6.cathode, D7.cathode, D8.cathode, K4.COIL1, K3.COIL1, K2.COIL1, U3.input_voltage
  N11: K5.A, J5.pin3
  N12: K5.C1, K5.C2, J5.pin1
  N13: K5.COIL2, Q5.C, D5.anode
  N14: K5.B, J5.pin2
  N15: K6.A, J6.pin3
  N16: K6.C1, K6.C2, J6.pin1
  N17: K6.COIL2, K7.COIL2, Q6.C, Q7.C, D6.anode, D7.anode
  N18: K6.B, J6.pin2
  N19: K1.A, J1.pin3
  N20: K1.C1, K1.C2, J1.pin1
  N21: K1.COIL2, Q1.C, D1.anode
  N22: K1.B, J1.pin2
  N23: K7.A, J7.pin3
  N24: K7.C1, K7.C2, J7.pin1
  N25: K7.B, J7.pin2
  N26: K8.A, J8.pin3
  N27: K8.C1, K8.C2, J8.pin1
  N28: K8.COIL2, Q8.C, D8.anode
  N29: K8.B, J8.pin2
  N30: OI-O_8.Pin_2, R2.5
  N31: OI-O_8.Pin_4, R10.Pin_1
  N32: OI-O_8.Pin_3, Q8.B
  N33: OI-O_6.Pin_2, R2.3
  N34: OI-O_6.Pin_4, R8.Pin_1
  N35: OI-O_6.Pin_3, Q6.B
  N36: OI-O_7.Pin_2, R2.4
  N37: OI-O_7.Pin_4, R9.Pin_1
  N38: OI-O_7.Pin_3, Q7.B
  N39: R1.2, OI-O_1.Pin_2
  N40: R1.3, OI-O_2.Pin_2
  N41: R1.4, OI-O_3.Pin_2
  N42: R1.5, OI-O_4.Pin_2
  N43: R2.2, OI-O_5.Pin_2
  N44: OI-O_3.Pin_4, R5.Pin_1
  N45: OI-O_3.Pin_3, Q3.B
  N46: OI-O_4.Pin_4, R6.Pin_1
  N47: OI-O_4.Pin_3, Q4.B
  N48: OI-O_5.Pin_4, R7.Pin_1
  N49: OI-O_5.Pin_3, Q5.B
  N50: OI-O_2.Pin_4, R4.Pin_1
  N51: OI-O_2.Pin_3, Q2.B
  N52: OI-O_1.Pin_4, R3.Pin_1
  N53: OI-O_1.Pin_3, Q1.B
  N54: Q2.C, D3.anode, K2.COIL2
  N55: Q3.C, D2.anode, K3.COIL2
  N56: Q4.C, D4.anode, K4.COIL2
  N57: K4.A, J4.pin3
  N58: K4.C1, K4.C2, J4.pin1
  N59: K4.B, J4.pin2
  N60: K3.A, J3.pin3
  N61: K3.C1, K3.C2, J3.pin1
  N62: K3.B, J3.pin2
  N63: J2.pin1, K2.C1, K2.C2
  N64: J2.pin2, K2.B
  N65: J2.pin3, K2.A
