# Fritzing sketch id2552_MEGR3156_0 (saved by Fritzing 0.9.3b)

parts:
  Part1 = Arduino Uno (Rev3)  # not connected
  Part2 = Arduino Ethernet Shield (Rev3)
  J3 = Basic Servo
  J4 = Basic Servo
  BAT1 = BC9VPC [package=bc9vpc]
  VCC1 = 4 x AAA Battery Mount  # not connected
  J6 = Basic Servo
  J7 = Basic Servo
  J8 = Basic Servo
  R1 = Dial Potentiometer with switch  # not connected
  R2 = Dial Potentiometer with switch  # not connected
  R3 = Dial Potentiometer with switch  # not connected
  R4 = Dial Potentiometer with switch  # not connected
  R5 = Dial Potentiometer with switch  # not connected

nets:
  GND: Part2.GND, J3.gnd, J4.gnd, BAT1.V-, J8.gnd
  N1: Part2.SPI/D12, J7.pulse
  N2: Part2.SPI/D13, J6.pulse
  N3: Part2.PWM_D3, J8.pulse
  N4: Part2.PWM_D5, J4.pulse
  N5: Part2.PWM_D6, J3.pulse
