# Fritzing sketch id2553_proyecto_pirata_0 (saved by Fritzing 0.9.3b)
breadboards: 1

parts:
  Componente1 = Arduino Uno (Rev3)
  R1 = Resistor [tolerance=±5% resistance=220 package=THT]
  J1 = Piezo Speaker

nets:
  N1: Componente1.D9_PWM, R1.Pin_1
  N2: Componente1.GND, J1.pin1
  N3: R1.Pin_0, J1.pin2
