# Fritzing sketch id2554_melodic_scribe_0 (saved by Fritzing 0.8.4b)
circuit board: 10.2869cm x 4.24744cm
breadboards: 1

parts:
  Teensy1 = Teensy 2.0
  Relay_833H-1C-C = Relay [part_number=833H-1C-C package=THT]
  D1 = Rectifier Diode [part_number=1N4001 package="300 mil [THT]"]
  R1 = Resistor [tolerance=±5% resistance=100 package=THT]
  Relay_833H-1C-C_2 = Relay [part_number=833H-1C-C package=THT]
  D3 = Rectifier Diode [part_number=1N4001 package="300 mil [THT]"]
  R3 = Resistor [tolerance=±5% resistance=100 package=THT]
  Relay_833H-1C-C_3 = Relay [part_number=833H-1C-C package=THT]
  D4 = Rectifier Diode [part_number=1N4001 package="300 mil [THT]"]
  R4 = Resistor [tolerance=±5% resistance=100 package=THT]
  Power_plug1 = Power plug
  M1 = DC Motor
  M2 = DC Motor
  Q1 = NPN-Transistor [package="TO92 [THT]"]
  Q3 = NPN-Transistor [package="TO92 [THT]"]
  Q4 = NPN-Transistor [package="TO92 [THT]"]

nets (from the breadboard view):
  N1: Teensy1.GND, Q1.E, Q3.E, Q4.E
  N2: Teensy1.B2, R1.Pin_0, R4.Pin_0
  N3: Teensy1.B7, R3.Pin_0
  N4: Teensy1.VCC, Relay_833H-1C-C.COIL1, D1.anode, Relay_833H-1C-C_2.COIL1, D3.anode, Relay_833H-1C-C_3.COIL1, D4.anode
  N5: Relay_833H-1C-C.A, Relay_833H-1C-C_2.B, Relay_833H-1C-C_3.A, Power_plug1.GND
  N6: Relay_833H-1C-C.C1, Relay_833H-1C-C.C2, M1.pin_1
  N7: Relay_833H-1C-C.COIL2, D1.cathode, Q1.C
  N8: Relay_833H-1C-C.B, Relay_833H-1C-C_3.B, Power_plug1.VCC, M2.pin_2
  N9: R1.Pin_1, Q1.B
  N10: Relay_833H-1C-C_2.C1, Relay_833H-1C-C_2.C2, M2.pin_1
  N11: Relay_833H-1C-C_2.COIL2, D3.cathode, Q3.C
  N12: R3.Pin_1, Q3.B
  N13: Relay_833H-1C-C_3.C1, Relay_833H-1C-C_3.C2, M1.pin_2
  N14: Relay_833H-1C-C_3.COIL2, D4.cathode, Q4.C
  N15: R4.Pin_1, Q4.B
