# Fritzing sketch id2555_LED_constantly_on (saved by Fritzing 0.9.3b)
breadboards: 1

parts:
  Arduino_Mega_2560 = Arduino Mega 2560 (Rev3)
  LED1 = LED - 5mm [color="Red (633nm)" package="5 mm [THT]"]
  R1 = Resistor [tolerance=±5% resistance=220 package=THT]

nets:
  N1: Arduino_Mega_2560.5V, R1.Pin_1
  N2: Arduino_Mega_2560.GND, LED1.cathode
  N3: LED1.anode, R1.Pin_0

notes:
  LED voltage 1.8 V
  LED current 15 mA
