# Fritzing sketch id2555_Lampu_0 (saved by Fritzing 0.9.3b)
breadboards: 1

parts:
  Part1 = Arduino Uno (Rev3)
  R1 = Resistor [tolerance=±5% resistance=4.7k package=THT]
  R2 = Resistor [tolerance=±5% resistance=220 package=THT]  # not connected
  R3 = Resistor [tolerance=±5% resistance=330 package=THT]
  LED2 = LED - 5mm [color="Red (633nm)" package="5 mm [THT]"]
  R4 = Resistor [tolerance=±5% resistance=330 package=THT]
  LED3 = LED - 5mm [color="Blue (430nm)" package="5 mm [THT]"]
  R5 = Resistor [tolerance=±5% resistance=330 package=THT]
  LED4 = LED - 5mm [color="Green (555nm)" package="5 mm [THT]"]
  R6 = Resistor [tolerance=±5% resistance=330 package=THT]
  LED5 = LED - 5mm [color="Red (633nm)" package="5 mm [THT]"]
  R7 = Photocell (LDR) [package=THT]

nets:
  N1: Part1.A0, R1.Pin_0, R7.pin_1
  N2: Part1.D3_PWM, R3.Pin_0
  N3: Part1.D4, R4.Pin_0
  N4: Part1.D5_PWM, R5.Pin_0
  N5: Part1.D6_PWM, R6.Pin_0
  N6: Part1.5V, R7.pin_0
  N7: Part1.GND, R1.Pin_1, LED2.anode, LED3.anode, LED4.anode, LED5.anode
  N8: R3.Pin_1, LED2.cathode
  N9: R4.Pin_1, LED3.cathode
  N10: R5.Pin_1, LED4.cathode
  N11: R6.Pin_1, LED5.cathode
