# Fritzing sketch id2556_proyecto_0 (saved by Fritzing 0.9.3b)
breadboards: 1

parts:
  Part1 = Arduino Mega 2560 (Rev3)
  Q1 = npn-Powertransistor [package="TO220 [THT]"]
  V1 = DC Power [voltage=12V]
  R2 = Resistor [tolerance=±5% resistance=2.2k package=THT]
  LED1 = LEDs [package=led10mm]
  S1 = Pushbutton [package=THT]
  R3 = Resistor [tolerance=±5% resistance=220 package=THT]

nets:
  N1: Part1.5V, S1.leg0
  N2: Part1.GND, Q1.emitter, V1.V-, R3.Pin_0
  N3: Part1.D5_PWM, S1.leg1, R3.Pin_1
  N4: Part1.D7_PWM, R2.Pin_0
  N5: Q1.base, R2.Pin_1
  N6: Q1.collector, LED1.A
  N7: V1.V+, LED1.C
