# Fritzing sketch id2557_Untitled_Sketch (saved by Fritzing 0.9.3b)
circuit board: 8.46667cm x 5.64444cm
breadboards: 1

parts:
  Componente1 = Arduino Uno (Rev3)
  R2 = Resistor [tolerance=±5% resistance=220 package=THT]
  LED1 = LED - 5mm [color="Red (633nm)" package="5 mm [THT]"]
  S1 = Pushbutton [package=THT]
  R3 = Resistor [tolerance=±5% resistance=10k package=THT]

nets:
  N1: Componente1.D8, S1.leg1, R3.Pin_1
  N2: Componente1.D4, LED1.anode
  N3: Componente1.5V, S1.leg0
  N4: Componente1.GND, R2.Pin_0, R3.Pin_0
  N5: R2.Pin_1, LED1.cathode
