# Fritzing sketch id2557_memory_0 (saved by Fritzing 0.9.0b)
breadboards: 1

parts:
  Raspberry_Pi1 = Raspberry_Pi_B+
  R7 = Resistor [tolerance=±5% resistance=1k package=THT]
  R9 = Resistor [tolerance=±5% resistance=1k package=THT]
  R11 = Resistor [tolerance=±5% resistance=1k package=THT]
  R12 = Resistor [tolerance=±5% resistance=1k package=THT]
  R19 = Resistor [tolerance=±5% resistance=1k package=THT]
  R20 = Resistor [tolerance=±5% resistance=1k package=THT]
  R21 = Resistor [tolerance=±5% resistance=1k package=THT]
  R22 = Resistor [tolerance=±5% resistance=1k package=THT]
  LED1 = LED - 5mm [color="Red (633nm)" package="5 mm [THT]"]
  LED2 = LED - 5mm [color="Yellow (595nm)" package="5 mm [THT]"]
  LED3 = LED - 5mm [color="Green (570nm)" package="5 mm [THT]"]
  LED4 = LED - 5mm [color="Blue (525nm)" package="5 mm [THT]"]
  S1 = Pushbutton [package="[THT]"]
  S2 = Pushbutton [package="[THT]"]
  S3 = Pushbutton [package="[THT]"]
  S4 = Pushbutton [package="[THT]"]
  U1 = Buzzer [chip_label=Buzzer]
  R27 = Resistor [tolerance=±5% resistance=220 package=THT]

nets:
  N1: Raspberry_Pi1.connector0, S1.Pin_1, S1.Pin_2, S2.Pin_1, S2.Pin_2, S3.Pin_1, S3.Pin_2, S4.Pin_1, S4.Pin_2
  N2: Raspberry_Pi1.connector5, R7.Pin_1
  N3: Raspberry_Pi1.connector6, R9.Pin_1
  N4: Raspberry_Pi1.connector17, R19.Pin_1
  N5: Raspberry_Pi1.connector18, R22.Pin_1
  N6: Raspberry_Pi1.connector20, U1.connector0
  N7: Raspberry_Pi1.connector21, R21.Pin_1
  N8: Raspberry_Pi1.connector22, R20.Pin_1
  N9: Raspberry_Pi1.connector31, R12.Pin_1
  N10: Raspberry_Pi1.connector32, R11.Pin_1
  N11: Raspberry_Pi1.connector37, LED1.cathode, LED2.cathode, LED3.cathode, LED4.cathode, R27.Pin_1
  N12: R7.Pin_0, LED1.anode
  N13: R9.Pin_0, LED2.anode
  N14: R11.Pin_0, LED3.anode
  N15: R12.Pin_0, LED4.anode
  N16: R19.Pin_0, S1.Pin_3, S1.Pin_4
  N17: R20.Pin_0, S2.Pin_3, S2.Pin_4
  N18: R21.Pin_0, S4.Pin_3, S4.Pin_4
  N19: R22.Pin_0, S3.Pin_3, S3.Pin_4
  N20: U1.connector1, R27.Pin_0

notes:
  Memory game
  8x 1K Ohms resistor
  4x 4 pins push button
  4x LED (different colors)
  1x Buzzer
  1x 220 Ohms resistor for buzzer
  Single core wires (male-male and male-female)
