# Fritzing sketch id2559_arduinoo_0 (saved by Fritzing 0.7.12b)
breadboards: 1

parts:
  Arduino1 = Arduino
  U1 = mystery part, 3 pins [chip_label=?]
  R1 = Resistor [tolerance=±5% resistance=220 package=THT]
  LED1 = LED - 5mm [color="Red (633nm)" package="5 mm [THT]"]

nets:
  N1: Arduino1.D13, LED1.cathode
  N2: Arduino1.+5V, U1.pin3
  N3: U1.pin2, R1.Pin_0
