# Fritzing sketch id255_Adjustable_LED_0 (saved by Fritzing 0.8.3b)
breadboards: 1

parts:
  LED1 = LED - 5mm [color="Red (633nm)" package="5 mm [THT]"]
  R1 = TRIMPOT [package=trim_pot_pth]  # not connected
  VCC1 = Battery block 9V

nets:
  N1: LED1.cathode, VCC1.+
