# Fritzing sketch id2560_Alphanumeric_hello_0 (saved by Fritzing 0.9.2b)
circuit board: 8.46667cm x 5.64444cm
breadboards: 1

parts:
  Part1 = Arduino Uno (Rev3)
  LTP587HR = Alphanumeric LED Display [package=alphanumeric]

nets:
  N1: Part1.D8, LTP587HR.N
  N2: Part1.D9_PWM, LTP587HR.H
  N3: Part1.D10_PWM/SS, LTP587HR.L
  N4: Part1.D11_PWM/MOSI, LTP587HR.D1
  N5: Part1.D2, LTP587HR.VCC
  N6: Part1.D3_PWM, LTP587HR.F, LTP587HR.G1
  N7: Part1.D4, LTP587HR.B
  N8: Part1.D5_PWM, LTP587HR.A2
  N9: Part1.D6_PWM, LTP587HR.K
  N10: Part1.3V3, LTP587HR.J

notes:
  This circuit is based on the LTP587HR {Not the display in the diagram}
  *Pinout: Arduino Pins -16 Segment Display
  (2-H, 3-G, 4-U, 5-P, 6-C, 7-D, 8-T, 9-M, 10-S, 11-F)
