# Fritzing sketch id2562_Metal_Detector_0 (saved by Fritzing 0.3.14b)
breadboards: 1

parts:
  L1 = Inductor [package="400 mil [THT]"]
  L2 = Inductor [package="400 mil [THT]"]
  L3 = Inductor [package="400 mil [THT]"]
  L4 = Inductor [package="400 mil [THT]"]
  L5 = Inductor [package="400 mil [THT]"]
  L6 = Inductor [package="400 mil [THT]"]
  L7 = Inductor [package="400 mil [THT]"]
  S1 = Reed switch [package=THT]
  VCC1 = obsolete Battery
  PWR = Blue LED - 5mm
  S2 = Toggle Switch [package=THT]
  R1 = Resistor [resistance=220 package=THT]
  SENSITIVITY = Rotary Potentiometer (Large) [package=THT]
  LED3 = Red LED - 5mm
  LED5 = Red LED - 5mm
  LED6 = Red LED - 5mm
  J1 = Piezo Speaker
  TEST = Pushbutton [package="[THT]"]

nets:
  N1: L1.pin_0, SENSITIVITY.leg2, TEST.Pin_1, TEST.Pin_2
  N2: L1.pin_1, L2.pin_0
  N3: L2.pin_1, L3.pin_0
  N4: L3.pin_1, L4.pin_1
  N5: L4.pin_0, L5.pin_1
  N6: L5.pin_0, L6.pin_1
  N7: L6.pin_0, L7.pin_1
  N8: L7.pin_0, VCC1.+, J1.pin2
  N9: S1.pin_1, LED3.cathode, LED5.cathode, LED6.cathode
  N10: S1.pin_2, PWR.anode, SENSITIVITY.wiper, TEST.Pin_3, TEST.Pin_4
  N11: VCC1.-, R1.Pin_1
  N12: PWR.cathode, S2.L2
  N13: S2.COM, R1.Pin_0
  N14: LED3.anode, LED5.anode, LED6.anode, J1.pin1
