# Fritzing sketch id2563_Light_Table_Circuit_B (saved by Fritzing 0.6.3b)
breadboards: 1

parts:
  PhotoTransistor = Photocell (LDR) [package=THT]
  LED1 = LED - 5mm [color="Red (633nm)" package="5 mm [THT]"]
  LED2 = LED - 5mm [color="Red (633nm)" package="5 mm [THT]"]
  LED3 = LED - 5mm [color="Red (633nm)" package="5 mm [THT]"]
  LED4 = LED - 5mm [color="Red (633nm)" package="5 mm [THT]"]
  1_Kohm = Resistor [tolerance=±5% resistance=220 package=THT]
  VCC = Battery
  2N3904 = NPN-Transistor [package="TO92 [THT]"]

nets:
  N1: PhotoTransistor.pin_0, LED1.anode, LED2.anode, LED3.anode, LED4.anode, VCC.+
  N2: PhotoTransistor.pin_1, 1_Kohm.Pin_1, 2N3904.B
  N3: LED1.cathode, LED2.cathode, LED3.cathode, LED4.cathode, 2N3904.E
  N4: 1_Kohm.Pin_0, VCC.-, 2N3904.C

notes:
  LED Shadow Sensor
  Created by: TXTCLA55 2011
  Collector
