# Fritzing sketch id2564_MetOnline_0 (saved by Fritzing 0.9.3b)
breadboards: 1

parts:
  RHT1 = Humidity and Temperature Sensor RHT03 [part_number=DHT11]
  Componente1 = Arduino Ethernet Shield (Rev3)
  Componente2 = LCD1602-I2C_
  S1 = Pushbutton [package="[THT]"]
  R1 = Resistor [tolerance=±5% resistance=10k package=THT]
  4_Channel_Relay1 = richardbruneau00

nets:
  VCC: RHT1.Vcc, Componente1.5V, Componente2.connector1, S1.Pin_3, S1.Pin_4, 4_Channel_Relay1.connector13
  N1: RHT1.Data-signal, Componente1.D2
  N2: RHT1.GND_1, Componente1.GND, Componente2.connector0, R1.Pin_1, 4_Channel_Relay1.connector8
  N3: Componente1.D8, 4_Channel_Relay1.connector12
  N4: Componente1.PWM_D9, S1.Pin_1, S1.Pin_2, R1.Pin_0
  N5: Componente1.A4/SDA, Componente2.connector2
  N6: Componente1.A5/SCL, Componente2.connector3
  N7: Componente1.PWM_D5, 4_Channel_Relay1.connector9
  N8: Componente1.PWM_D6, 4_Channel_Relay1.connector10
  N9: Componente1.D7, 4_Channel_Relay1.connector11
  N10: 4_Channel_Relay1.connector14, 4_Channel_Relay1.connector15
