# Fritzing sketch id2565_metronome_0 (saved by Fritzing 0.7.12b)
breadboards: 1

parts:
  Arduino1 = Arduino
  LCD1 = LCD screen
  R1 = Rotary Potentiometer (Small)
  S1 = Pushbutton [package=THT]
  S2 = Pushbutton [package=THT]
  J1 = Piezo Speaker
  LED1 = white LED - 5mm [package="5 mm [THT]"]
  R3 = Resistor [tolerance=±5% resistance=10k package=THT]
  R4 = Resistor [tolerance=±5% resistance=10k package=THT]
  R5 = Resistor [tolerance=±5% resistance=560 package=THT]

nets:
  N1: Arduino1.D12, LCD1.RS
  N2: Arduino1.D11, LCD1.E
  N3: Arduino1.D9, S2.leg0, R3.Pin_0
  N4: Arduino1.D8, S1.leg1, R4.Pin_1
  N5: Arduino1.D6, J1.pin2, R5.Pin_0
  N6: Arduino1.D5, LCD1.DB4
  N7: Arduino1.D4, LCD1.DB5
  N8: Arduino1.D3, LCD1.DB6
  N9: Arduino1.D2, LCD1.DB7
  +5V: Arduino1.+5V, LCD1.VDD, R1.leg1, S1.leg0, S2.leg1
  GND: Arduino1.GND, LCD1.VSS, LCD1.R/W, R1.leg2, J1.pin1, LED1.anode, R3.Pin_1, R4.Pin_0
  N10: LCD1.V0, R1.wiper
  N11: LED1.cathode, R5.Pin_1
