# Fritzing sketch id2566_sketch_0 (saved by Fritzing 0.7.10b)
breadboards: 1

parts:
  U1 = 555 Timer [package="DIP8 [THT]"]
  R1 = Resistor [tolerance=±5% resistance=1k package=THT]
  R2 = Resistor [tolerance=±5% resistance=1k package=THT]
  R3 = Rotary Potentiometer (Small) [maximum_resistance=100kΩ]
  C1 = Electrolytic Capacitor [capacitance=22µF voltage=16V package="100 mil [THT, electrolytic]"]
  LED1 = LED - 5mm [color="Red (633nm)" package="5 mm [THT]"]
  C2 = Electrolytic Capacitor [capacitance=22µF voltage=16V package="100 mil [THT, electrolytic]"]
  R4 = Resistor [tolerance=±5% resistance=1k package=THT]
  LED2 = LED - 5mm [color="Red (633nm)" package="5 mm [THT]"]
  SPKR1 = Loudspeaker
  VCC1 = Battery block 9V

nets:
  N1: U1.Ground, C2.-, LED2.anode, SPKR1.pin2, VCC1.-
  N2: U1.Trigger, U1.Threshold, R3.leg2, C2.+
  N3: U1.Output, C1.-, LED1.cathode, R4.Pin_1
  N4: U1.Reset, U1.Vcc_Supply_Voltage, R1.Pin_1, R2.Pin_1, VCC1.+
  N5: U1.Discharge, R1.Pin_0, R3.wiper
  N6: R2.Pin_0, LED1.anode
  N7: C1.+, SPKR1.pin1
  N8: R4.Pin_0, LED2.cathode
