# Fritzing sketch id2567_Arduino_Uno_r3_with_RFID_RC522_0 (saved by Fritzing 0.9.0b)
breadboards: 1

parts:
  Part2 = RFID-RC522
  Part1 = Arduino Uno (Rev3) - ICSP

nets:
  N1: Part2.connector8, Part1.D10_PWM/SS
  N2: Part2.connector9, Part1.D13/SCK
  N3: Part2.connector10, Part1.D11_PWM/MOSI
  N4: Part2.connector11, Part1.D12/MISO
  N5: Part2.connector13, Part1.GND
  N6: Part2.connector14, Part1.D9_PWM
  N7: Part2.connector15, Part1.3V3
