# Fritzing sketch id2568_MH_Z14_setup_0 (saved by Fritzing 0.7.11b)
breadboards: 1

parts:
  IC1 = IC, DIP package, 8 pins [chip_label=741CN]  # not connected
  MH-Z1 = generic_ic_dip_16_300mil.fzp [part_number=MH-Z14]
  R1 = Resistor [tolerance=±5% resistance=2M package=THT]
  R2 = Resistor [tolerance=±5% resistance=1M package=THT]
  Arduino1 = Arduino
  R3 = Resistor [tolerance=±5% resistance=2M package=THT]
  R4 = Resistor [tolerance=±5% resistance=1M package=THT]

nets:
  N1: MH-Z1.connector1, R1.Pin_1, Arduino1.GND
  N2: MH-Z1.connector13, R3.Pin_0, R4.Pin_0
  N3: MH-Z1.connector14, Arduino1.+5V, R3.Pin_1
  N4: R1.Pin_0, R2.Pin_0
  N5: R2.Pin_1, Arduino1.D2
  N6: Arduino1.D3, R4.Pin_1

notes:
  Voltage divider
  100 MOhm - 200 MOhm
  => 67% of 5V = 3.3V
  Opamp
  100 MOhm - 200 MOhm
  => 150% of 3.5V (capped to 5V) = 5V
