# Fritzing sketch id2570_Untitled_234_0 (saved by Fritzing 0.9.3b)
breadboards: 1

parts:
  Part1 = Arduino Uno (Rev3)
  S1 = Pushbutton [package="[THT]"]
  S2 = Pushbutton [package="[THT]"]
  S3 = Toggle Switch [package=THT]
  Part2 = EasyDriver_v44
  R1 = Resistor [tolerance=±5% resistance=4.7k package=THT]
  M1 = Stepper Motor - Bipolar
  BAT3 = BC9VPC [package=bc9vpc]

nets:
  N1: Part1.D8, Part2.ENABLE
  N2: Part1.D11_PWM/MOSI, S1.Pin_1, S1.Pin_2
  N3: Part1.D12/MISO, S2.Pin_3, S2.Pin_4
  N4: Part1.D2, Part2.DIR
  N5: Part1.D5_PWM, Part2.STEP
  N6: Part1.D7, S3.COM, R1.Pin_0
  5V: Part1.5V, Part2.VCC, R1.Pin_1
  GND: Part1.GND, S1.Pin_3, S1.Pin_4, S2.Pin_1, S2.Pin_2, S3.L1, Part2.GND, BAT3.V-
  N7: Part2.V+, BAT3.V+
  N8: Part2.OUT2A, M1.A
  N9: Part2.OUT2B, M1.C
  N10: Part2.OUT1A, M1.B
  N11: Part2.OUT1B, M1.D
