# Fritzing sketch id2571_forward_voltage (saved by Fritzing 0.6.3b)
breadboards: 1

parts:
  VCC2 = Battery
  VCC1 = Battery
  R1 = Resistor [tolerance=±5% resistance=1k package=THT]
  LED1 = LED - 5mm [color="Green (555nm)" package="5 mm [THT]"]

nets:
  N1: VCC2.+, R1.Pin_1, LED1.anode
  N2: VCC1.-, LED1.cathode
  N3: VCC1.+, R1.Pin_0
