# Fritzing sketch id2572_hola_mundo_0 (saved by Fritzing 0.9.2b)
breadboards: 1

parts:
  Parte1 = Arduino Uno (Rev3)
  LED1 = smd LED [color="Red (633nm)" package="0805 [SMD]"]
  R1 = Resistor [tolerance=±5% resistance=220 package=THT]

nets:
  N1: Parte1.D13/SCK, R1.Pin_0
  N2: Parte1.GND, LED1.cathode
  N3: LED1.anode, R1.Pin_1
