# Fritzing sketch id2573_Proy_luz_0 (saved by Fritzing 0.9.2b)
breadboards: 1

parts:
  Parte1 = Arduino Uno (Rev3)
  LED1 = LED - 5mm [color="Red (633nm)" package="5 mm [THT]"]
  R1 = Resistor [tolerance=±5% resistance=220 package=THT]

nets:
  N1: Parte1.D13/SCK, LED1.cathode
  N2: LED1.anode, R1.Pin_0
