# Fritzing sketch id2575_LED_Lauflicht (saved by Fritzing 0.9.3b)
breadboards: 1

parts:
  Bauteil1 = Arduino Mega 2560 (Rev3)
  LED1 = LED - 5mm [color="White (6500K)" package="5 mm [THT]"]
  R1 = Resistor [tolerance=±5% resistance=22 package=THT]
  LED2 = LED - 5mm [color="White (6500K)" package="5 mm [THT]"]
  LED3 = LED - 5mm [color="White (6500K)" package="5 mm [THT]"]
  LED4 = LED - 5mm [color="White (6500K)" package="5 mm [THT]"]
  LED5 = LED - 5mm [color="White (6500K)" package="5 mm [THT]"]
  LED6 = LED - 5mm [color="White (6500K)" package="5 mm [THT]"]
  R2 = Resistor [tolerance=±5% resistance=22 package=THT]
  R3 = Resistor [tolerance=±5% resistance=22 package=THT]
  R4 = Resistor [tolerance=±5% resistance=22 package=THT]
  R5 = Resistor [tolerance=±5% resistance=22 package=THT]
  R6 = Resistor [tolerance=±5% resistance=22 package=THT]
  LED7 = LED - 3mm [color="White (6500K)" package="3 mm [THT]"]
  LED8 = LED - 3mm [color="White (6500K)" package="3 mm [THT]"]
  LED9 = LED - 3mm [color="White (6500K)" package="3 mm [THT]"]
  LED10 = LED - 3mm [color="White (6500K)" package="3 mm [THT]"]
  LED11 = LED - 3mm [color="White (6500K)" package="3 mm [THT]"]
  LED12 = LED - 3mm [color="White (6500K)" package="3 mm [THT]"]
  R7 = Resistor [tolerance=±5% resistance=22 package=THT]
  R8 = Resistor [tolerance=±5% resistance=22 package=THT]
  R9 = Resistor [tolerance=±5% resistance=22 package=THT]
  R10 = Resistor [tolerance=±5% resistance=22 package=THT]
  R11 = Resistor [tolerance=±5% resistance=22 package=THT]
  R12 = Resistor [tolerance=±5% resistance=22 package=THT]

nets:
  N1: Bauteil1.D42, R6.Pin_1
  N2: Bauteil1.D43, R7.Pin_1
  N3: Bauteil1.D44, R5.Pin_1
  N4: Bauteil1.D45, R8.Pin_1
  N5: Bauteil1.D46, R4.Pin_1
  N6: Bauteil1.D47, R9.Pin_1
  N7: Bauteil1.D48, R3.Pin_1
  N8: Bauteil1.D49, R10.Pin_1
  N9: Bauteil1.D50, R2.Pin_1
  N10: Bauteil1.D52, R1.Pin_1
  N11: Bauteil1.D53, R12.Pin_1
  N12: Bauteil1.GND, LED1.cathode, LED3.cathode, LED4.cathode, LED6.cathode, LED7.cathode, LED8.cathode, LED9.cathode, LED10.cathode, LED11.cathode, LED12.cathode
  N13: LED1.anode, R1.Pin_0
  N14: LED2.anode, R2.Pin_0
  N15: LED3.anode, R3.Pin_0
  N16: LED4.anode, R4.Pin_0
  N17: LED5.anode, R5.Pin_0
  N18: LED6.anode, R6.Pin_0
  N19: LED7.anode, R12.Pin_0
  N20: LED8.anode, R9.Pin_0
  N21: LED9.anode, R10.Pin_0
  N22: LED10.anode, R11.Pin_0
  N23: LED11.anode, R8.Pin_0
  N24: LED12.anode, R7.Pin_0
