# Fritzing sketch id2575_tmp_10857_NA_Miata_48_pin_382148797_0 (saved by Fritzing 0.9.2b)
circuit board: 4cm x 10cm
breadboards: 1

parts:
  J1 = shrouded pin header, 40 pins [form="♂ (shrouded male)"]  # not connected
  J3 = female pin header, 1 pin [form="♀ (female)"]  # not connected
  J4 = female pin header, 1 pin [form="♀ (female)"]
  J5 = female pin header, 1 pin [form="♀ (female)"]  # not connected
  J6 = female pin header, 1 pin [form="♀ (female)"]  # not connected
  J7 = female pin header, 1 pin [form="♀ (female)"]  # not connected
  J8 = female pin header, 1 pin [form="♀ (female)"]  # not connected
  J9 = female pin header, 1 pin [form="♀ (female)"]  # not connected
  J10 = female pin header, 1 pin [form="♀ (female)"]  # not connected
  J11 = female pin header, 1 pin [form="♀ (female)"]  # not connected
  J12 = female pin header, 1 pin [form="♀ (female)"]  # not connected
  J13 = female pin header, 1 pin [form="♀ (female)"]  # not connected
  J14 = female pin header, 1 pin [form="♀ (female)"]  # not connected
  J15 = female pin header, 1 pin [form="♀ (female)"]  # not connected
  J16 = female pin header, 1 pin [form="♀ (female)"]  # not connected
  J17 = female pin header, 1 pin [form="♀ (female)"]  # not connected
  J18 = female pin header, 1 pin [form="♀ (female)"]  # not connected
  J19 = female pin header, 1 pin [form="♀ (female)"]  # not connected
  J20 = female pin header, 1 pin [form="♀ (female)"]  # not connected
  J21 = female pin header, 1 pin [form="♀ (female)"]  # not connected
  J22 = female pin header, 1 pin [form="♀ (female)"]  # not connected
  J23 = female pin header, 1 pin [form="♀ (female)"]  # not connected
  J24 = female pin header, 1 pin [form="♀ (female)"]  # not connected
  J25 = female pin header, 1 pin [form="♀ (female)"]  # not connected
  J26 = female pin header, 1 pin [form="♀ (female)"]  # not connected
  J27 = female pin header, 1 pin [form="♀ (female)"]  # not connected
  J28 = female pin header, 1 pin [form="♀ (female)"]  # not connected
  JP1 = Header 3 [package=screwterminal-3.5mm-3_lock.007s]  # not connected
  JP2 = Header 2 [package=screwterminal-3.5mm-2_lock]
  J29 = female pin header, 1 pin [form="♀ (female)"]  # not connected
  J30 = female pin header, 1 pin [form="♀ (female)"]  # not connected
  J31 = female pin header, 1 pin [form="♀ (female)"]  # not connected
  J32 = female pin header, 1 pin [form="♀ (female)"]  # not connected
  J33 = female pin header, 1 pin [form="♀ (female)"]  # not connected
  J34 = female pin header, 1 pin [form="♀ (female)"]  # not connected
  J35 = female pin header, 1 pin [form="♀ (female)"]  # not connected
  J36 = female pin header, 1 pin [form="♀ (female)"]  # not connected
  J37 = female pin header, 1 pin [form="♀ (female)"]  # not connected
  J38 = female pin header, 1 pin [form="♀ (female)"]  # not connected

nets:
  N1: J4.pin1, JP2.2
  GND: JP2.1

notes:
  1A
  2A
