# Fritzing sketch id2577_Tutoorial_1_LDR_Ex_1Sketch_0 (saved by Fritzing 0.9.2b)
breadboards: 1

parts:
  R2 = Resistor [tolerance=±5% resistance=10k package=THT]
  R3 = Photocell (LDR) [package=THT]

nets:
  N1: R2.Pin_0, R3.pin_1
