# Fritzing sketch id2578_Untitled_Sketch_2_0 (saved by Fritzing 0.9.2b)
breadboards: 1

parts:
  S1 = Pushbutton [package="[THT]"]
  元件1 = Arduino Uno (Rev3)
  R1 = Resistor [tolerance=±5% resistance=220 package=THT]
  R2 = Resistor [tolerance=±5% resistance=220 package=THT]
  LED1 = LED - 5mm [color="Red (633nm)" package="5 mm [THT]"]
  SPKR1 = Loudspeaker
  R3 = Resistor [tolerance=±5% resistance=220 package=THT]

nets:
  N1: S1.Pin_1, S1.Pin_2, 元件1.5V
  N2: S1.Pin_3, S1.Pin_4, 元件1.D13/SCK, R1.Pin_1
  N3: 元件1.A0, R3.Pin_1
  N4: 元件1.D12/MISO, R2.Pin_0
  N5: 元件1.GND, R1.Pin_0, LED1.anode, SPKR1.pin1
  N6: R2.Pin_1, LED1.cathode
  N7: SPKR1.pin2, R3.Pin_0
