# Fritzing sketch id2579_PicaxeControllerBase_0 (saved by Fritzing 0.9.3b)
circuit board: 2.05546cm x 1.78872cm
breadboards: 1

parts:
  IC1 = PICAXE-08 [package=THT]
  J1 = female pin header, 5 pins [form="♀ (female)"]
  R1 = Resistor [tolerance=±5% resistance=22k package="2010 [SMD]"]
  R2 = Resistor [tolerance=±5% resistance=10k package="2010 [SMD]"]
  J2 = female pin header, 2 pins [form="♀ (female)"]
  J3 = female pin header, 3 pins [form="♀ (female)"]

nets:
  N1: IC1.+V, J2.pin2
  N2: IC1.Serial_In, R1.Pin_1
  N3: IC1.In/Out_4, J1.pin1
  N4: IC1.In_3, J1.pin4
  N5: IC1.In/Out_2, J1.pin3
  N6: IC1.In/Out_1, J1.pin2
  N7: IC1.Serial_Out_/_Out_0, J1.pin5, J3.pin2
  N8: IC1.0V, R2.Pin_0, J2.pin1, J3.pin3
  N9: R1.Pin_0, R2.Pin_1, J3.pin1
