# Fritzing sketch id2580_PicaxeHalfConnect_0 (saved by Fritzing 0.9.3b)
circuit board: 2.04611cm x 1.79211cm
breadboards: 1

parts:
  U1 = 3.5mm Audio Jack [package=audio-jack]
  J1 = female pin header, 3 pins [form="♀ (female)"]
  J2 = female pin header, 5 pins [form="♀ (female)"]  # not connected

nets:
  N1: U1.RIGHT, J1.pin1
  N2: U1.SLEEVE, J1.pin2
  N3: U1.LEFT, J1.pin3
