# Fritzing sketch id2581_microSD_station_0 (saved by Fritzing 0.9.2b)
breadboards: 1

parts:
  Parte1 = Arduino Nano (Rev3.0)
  DHT1 = DHT22_Humidity_and_Temperature_Sensor
  R1 = Photocell (LDR) [package=THT]  # not connected
  R2 = Resistor [tolerance=±5% resistance=220 package=THT]  # not connected
  Parte3 = adafruit [part_number="Adafruit #264"]
  VCC1 = 4 x AAA Battery Mount

nets:
  N1: Parte1.GND, DHT1.connector3, VCC1.-
  N2: Parte1.VIN, VCC1.+
  N3: Parte1.5V, DHT1.connector1
  N4: Parte1.A5, Parte3.connector15
  N5: Parte1.A4, Parte3.connector14
