# Fritzing sketch id2582_schematics_0 (saved by Fritzing 0.9.0b)
breadboards: 1

parts:
  Microcontroller = Arduino Uno (Rev3)
  Distance_Sensor = Infrared Proximity Sensor
  Battery = 4 x AAA Battery Mount
  Voltage_Regulator_7V = Voltage Regulator [package=to-220-alt]
  Motor = DC Motor
  part = H-Bridge [package=THT]
  Motor_Encoder = ENCODER-QUADRATURE [package=encoder-16mm-quad]

nets:
  N1: Microcontroller.A0, Distance_Sensor.Vout
  GND: Microcontroller.GND, Distance_Sensor.GND, Battery.-, Voltage_Regulator_7V.GND, part.GND1, part.GND2
  N2: Microcontroller.D2, Motor_Encoder.A
  N3: Microcontroller.D3_PWM, Motor_Encoder.B
  N4: Microcontroller.D5_PWM, part.1A
  N5: Microcontroller.D6_PWM, part.2A
  N6: Microcontroller.D7, part.1_2EN
  5V: Microcontroller.5V, Distance_Sensor.Vcc, part.VCC1, Motor_Encoder.C
  N7: Microcontroller.VIN, Voltage_Regulator_7V.OUT, part.VCC2
  N8: Battery.+, Voltage_Regulator_7V.IN
  N9: Motor.pin_1, part.1Y
  N10: Motor.pin_2, part.2Y
