# Fritzing sketch id2583_miconucleus_t85_0 (saved by Fritzing 0.9.2b)
circuit board: 5.1cm x 2.8cm
breadboards: 1

parts:
  R1 = Resistor [tolerance=±5% resistance=68 package=THT]
  R2 = Resistor [tolerance=±5% resistance=68 package=THT]
  R3 = Resistor [tolerance=±5% resistance=2.2k package=THT]
  D1 = Zener Diode [part_number=1N4732A breakdown_voltage=3.6V package="300 mil [THT]"]
  D2 = Zener Diode [part_number=1N4732A breakdown_voltage=3.6V package="300 mil [THT]"]
  X1 = USB Connectors [package=usb-b-pth]
  U1 = attiny85 [package=dip]
  C1 = Ceramic Capacitor [capacitance=0.1µF package="100 mil [THT, multilayer]"]
  J1 = female pin header, 4 pins [form="♀ (female)"]
  J2 = female pin header, 4 pins [form="♀ (female)"]
  J3 = female pin header, 2 pins [form="♀ (female)"]
  R4 = Resistor [tolerance=±5% resistance=330 package=THT]
  LED1 = LED - 3mm [color="Blue (525nm)" package="3 mm [THT]"]

nets:
  N1: R1.Pin_0, R3.Pin_0, D2.cathode, X1.D-
  N2: R1.Pin_1, U1.Pin_2, J1.pin2
  N3: R2.Pin_0, D1.cathode, X1.D+
  N4: R2.Pin_1, U1.Pin_3, J1.pin3
  N5: R3.Pin_1, X1.VBUS, U1.Pin_8, C1.1, J2.pin1, J3.pin1, R4.Pin_0
  N6: D1.anode, D2.anode, X1.GND, U1.Pin_4, C1.0, J1.pin4, LED1.cathode
  N7: U1.Pin_1, J1.pin1, J3.pin2
  N8: U1.Pin_5, J2.pin4
  N9: U1.Pin_6, J2.pin3
  N10: U1.Pin_7, J2.pin2
  N11: R4.Pin_1, LED1.anode
