# Fritzing sketch id2584_miconucleus_t85_A_0 (saved by Fritzing 0.9.2b)
circuit board: 8.33164cm x 3.2cm
breadboards: 1

parts:
  X1 = USB Connectors [package=usb-b-pth]
  IC1 = ATtiny35_45_85
  J1 = AVR ICSP [form="♂ (shrouded male)"]
  S1 = Pushbutton [package="[THT]"]
  J2 = female pin header, 4 pins [form="♀ (female)"]
  J3 = female pin header, 4 pins [form="♀ (female)"]
  R1 = Resistor [tolerance=±5% resistance=10k package=THT]
  J4 = female pin header, 2 pins [form="♀ (female)"]
  C1 = Ceramic Capacitor [capacitance=0.1µF package="100 mil [THT, multilayer]"]
  C2 = Electrolytic Capacitor [capacitance=4.7µF package="100 mil [THT, electrolytic]"]
  R2 = Resistor [tolerance=±5% resistance=68 package=THT]
  R3 = Resistor [tolerance=±5% resistance=68 package=THT]
  R4 = Resistor [tolerance=±5% resistance=1.5k package=THT]
  D1 = Zener Diode [part_number=1N4732A breakdown_voltage=3.6V package="300 mil [THT]"]
  R5 = Resistor [tolerance=±5% resistance=1k package=THT]
  D2 = Zener Diode [part_number=1N4732A breakdown_voltage=3.6V package="300 mil [THT]"]
  LED1 = LED - 3mm [color="Green (570nm)" package="3 mm [THT]"]
  LED2 = LED - 3mm [color="Red (633nm)" package="3 mm [THT]"]
  R6 = Resistor [tolerance=±5% resistance=1k package=THT]

nets:
  N1: X1.D+, R3.Pin_0, D1.cathode
  N2: X1.D-, R2.Pin_0, R4.Pin_0, D2.cathode
  N3: X1.GND, IC1.connector3, J1.connector3, S1.Pin_3, S1.Pin_4, J2.pin4, C1.0, C2.-, D1.anode, D2.anode, LED1.anode, LED2.anode
  N4: X1.VBUS, IC1.connector7, J1.connector5, J3.pin1, R1.Pin_1, C1.1, C2.+, R4.Pin_1, R5.Pin_1
  N5: IC1.connector0, J1.connector2, S1.Pin_1, S1.Pin_2, J2.pin1, J4.pin2
  N6: IC1.connector1, J2.pin2, R2.Pin_1
  N7: IC1.connector2, J2.pin3, R3.Pin_1
  N8: IC1.connector4, J1.connector4, J3.pin4
  N9: IC1.connector5, J1.connector0, J3.pin3
  N10: IC1.connector6, J1.connector1, J3.pin2, R6.Pin_1
  N11: R1.Pin_0, J4.pin1
  N12: R5.Pin_0, LED1.cathode
  N13: LED2.cathode, R6.Pin_0
