# Fritzing sketch id2585_Untitled_Sketch_0 (saved by Fritzing 0.9.0b)
breadboards: 1

parts:
  MIC1 = Microphone
  Part1 = Arduino Uno (Rev3) - ICSP
  R1 = Resistor [tolerance=±5% resistance=10k package="0603 [SMD]"]

nets:
  N1: MIC1.pin1, Part1.GND
  N2: MIC1.pin2, Part1.A0, R1.Pin_0
  N3: Part1.5V, R1.Pin_1
