# Fritzing sketch id2586_microSD_breakout_0 (saved by Fritzing 0.8.6b)
circuit board: 1.72716cm x 2.21789cm

parts:
  microSD = microSD Socket [package="Molex 502774-0891 [SMD]"]
  J1 = female pin header, 6 pins [form="♀ (female)"]

nets:
  N1: microSD.CS, J1.pin6
  N2: microSD.DI, J1.pin5
  N3: microSD.VCC, J1.pin4
  N4: microSD.SCK, J1.pin3
  N5: microSD.GND, J1.pin2
  N6: microSD.DO, J1.pin1

notes:
  D0
  GND
  3V3
  SCK
  CS
  DI
