# Fritzing sketch id2587_microSD_adapter_for_rPi_0 (saved by Fritzing 0.8.3b)
circuit board: 2.42494cm x 1.7439cm
breadboards: 1

parts:
  U1 = microSD-socket-molex-502774-0891.fzp
  SD1 = SD Card [part_number=sdcard]

nets:
  N1: U1.connector1, SD1.connector4
  N2: U1.connector2, SD1.connector5
  N3: U1.connector3, SD1.connector7
  N4: U1.connector4, SD1.connector8
  N5: U1.connector5, U1.connector8, U1.connector9, U1.connector10, U1.connector11, SD1.connector6, SD1.connector9
  N6: U1.connector6, SD1.connector10
