# Fritzing sketch id2588_microSD_tested_OK_0 (saved by Fritzing 0.9.1b)
circuit board: 8.46667cm x 5.64444cm

parts:
  microSD1 = MicroSD_Breakout
  Part1 = Arduino Uno (Rev3)

nets:
  N1: microSD1.connector2, Part1.D4
  N2: microSD1.connector3, Part1.D11_PWM/MOSI
  N3: microSD1.connector4, Part1.D12/MISO
  N4: microSD1.connector5, Part1.D13/SCK
  N5: microSD1.connector6, Part1.GND
  N6: microSD1.connector8, Part1.5V
