# Fritzing sketch id2589_1_simpleledonoff (saved by Fritzing 0.9.3b)
breadboards: 1

parts:
  부품1 = Arduino Uno (Rev3)
  LED1 = LED - 5mm [color="Red (633nm)" package="5 mm [THT]"]
  R1 = Resistor [tolerance=±5% resistance=330 package=THT]

nets (from the breadboard view):
  N1: 부품1.GND, LED1.cathode
  N2: 부품1.D7, R1.Pin_1
  N3: LED1.anode, R1.Pin_0
