# Fritzing sketch id2589_MicroViewClock_schema_0 (saved by Fritzing 0.9.0b)
breadboards: 1

parts:
  Backup_battery_(3V) = Battery Holders [package=battcon_12mm]
  part = DS1302 [package="DIP8 [THT]"]
  part_2 = DC Power [voltage=5V]
  part_3 = MicroView [part_number=MicroView]
  32_768_KHz = CRYSTAL [package=tc26h]

nets:
  N1: Backup_battery_(3V).+, part.Vbat_-_Backup_Supply
  N2: Backup_battery_(3V).-, part.0V, part_2.V-, part_3.connector7
  N3: part.+V, part_2.V+, part_3.connector14
  N4: part.X1_-_Crystal, 32_768_KHz.2
  N5: part.X2_-_Crystal, 32_768_KHz.1
  N6: part.CE_-_Chip_Enable, part_3.connector13
  N7: part.I/O_-_SPI_Data_In/Out, part_3.connector12
  N8: part.SCLK_-_SPI_Clock, part_3.connector11
