# Fritzing sketch id258_MOSFET_H_Bridge_0 (saved by Fritzing 0.8.5b)
breadboards: 1

parts:
  U1 = Optocoupler [package=THT]
  U2 = Optocoupler [package=THT]
  R1 = Resistor [tolerance=±5% resistance=220 package=THT]
  R2 = Resistor [tolerance=±5% resistance=220 package=THT]
  Q3 = Basic FET P-Channel [package="TO220 [THT]"]
  Q1 = Basic FET N-Channel [package="TO220 [THT]"]
  Q4 = Basic FET P-Channel [package="TO220 [THT]"]
  Q2 = Basic FET N-Channel [package="TO220 [THT]"]
  M1 = DC Motor
  R3 = Resistor [tolerance=±5% resistance=10k package=THT]
  R4 = Resistor [tolerance=±5% resistance=10k package=THT]
  J1 = screw terminal, 3 pins
  VCC1 = Battery block 9V
  C1 = Electrolytic Capacitor [capacitance=22µF voltage=35V package="100 mil [THT, electrolytic]"]

nets:
  N1: U1.Pin_1, J1.pin2
  N2: U1.Pin_2, R1.Pin_0
  N3: U1.Pin_4, U2.Pin_4, Q1.source, Q2.source, C1.-
  N4: U1.Pin_5, Q3.gate, Q1.gate, R3.Pin_1
  N5: U2.Pin_1, J1.pin3
  N6: U2.Pin_2, R2.Pin_0
  N7: U2.Pin_5, Q4.gate, Q2.gate, R4.Pin_1
  N8: R1.Pin_1, R2.Pin_1, J1.pin1
  N9: Q3.drain, Q1.drain, M1.pin_2
  N10: Q3.source, Q4.source, R3.Pin_0, R4.Pin_0, VCC1.+, C1.+
  N11: Q4.drain, Q2.drain, M1.pin_1

notes:
  ERROR: ground must be connected to pin 4
  Here pin 4 is correctly on ground
