# Fritzing sketch id2591_Blowhard_Detector_0 (saved by Fritzing 0.9.2b)
breadboards: 1

parts:
  MVPROG1 = MicroViewProg [part_number=MicroView]
  J1 = Piezo Speaker
  MIC2 = Microphone
  R12 = Resistor [tolerance=±5% resistance=10k package=THT]
  R13 = Resistor [tolerance=±5% resistance=10k package=THT]
  R14 = Resistor [tolerance=±5% resistance=330k package=THT]
  C10 = Ceramic Capacitor [capacitance=100nF package="100 mil [THT, multilayer]"]
  C11 = Ceramic Capacitor [capacitance=100nF package="100 mil [THT, multilayer]"]
  Q4 = NPN-Transistor [package="TO92 [THT]"]
  U3 = LM386 [part_number=LM386 package=dip08]
  C15 = Electrolytic Capacitor [capacitance=100µF package="100 mil [THT, electrolytic]"]
  C16 = Ceramic Capacitor [capacitance=100nF package="100 mil [THT, multilayer]"]
  R17 = Resistor [tolerance=±5% resistance=10k package=THT]
  C17 = Electrolytic Capacitor [capacitance=0.1µF package="100 mil [THT, electrolytic]"]
  R18 = Resistor [tolerance=±5% resistance=10k package=THT]

nets:
  N1: MVPROG1.connector3, U3.+IN
  N2: MVPROG1.connector6, C11.0
  N3: MVPROG1.connector7, J1.pin1, MIC2.pin1, R12.Pin_1, R13.Pin_1, R14.Pin_0, C11.1, Q4.C, U3.-IN, U3.V-, R17.Pin_0, R18.Pin_0
  N4: MVPROG1.connector13, R12.Pin_0, R13.Pin_0, U3.V+
  N5: J1.pin2, C15.+
  N6: MIC2.pin2, C10.1
  N7: R14.Pin_1, C10.0, Q4.E, Q4.B
  N8: U3.GAIN, C17.-, C17.+
  N9: U3.OUT, C15.-, C16.0
  N10: U3.BP, R17.Pin_1
  N11: C16.1, R18.Pin_1
