# Fritzing sketch id2592_midi_0 (saved by Fritzing 0.8.5b)

parts:
  U1 = MIDI_CONN_FEMALE_SUPPORT [package=din_5_female_support]
  Part1 = Arduino Uno (Rev3)
  R1 = Resistor [tolerance=±5% resistance=220 package=THT]

nets:
  N1: U1.NC1, Part1.A4/SDA
  N2: U1.MIDI_IN, R1.Pin_1
  N3: U1.MIDI_OUT, Part1.D1/TX
  N4: Part1.5V, R1.Pin_0
