# Fritzing sketch id2593_Midi_In_Breadboard_0 (saved by Fritzing 0.7.10b)
breadboards: 1

parts:
  R1 = Resistor [tolerance=±5% resistance=220 package=THT]
  D1 = Rectifier Diode [part_number=N4748 package="300 mil [THT]"]
  R2 = Resistor [tolerance=±5% resistance=100k package=THT]
  R3 = Resistor [tolerance=±5% resistance=3.3k package=THT]
  U1 = Optocoupler [part_number=4N28 package=THT]
  DIN1 = DIN-5 jack (MIDI) [package=THT]
  Arduino1 = Arduino

nets:
  N1: R1.Pin_0, DIN1.4
  N2: R1.Pin_1, D1.cathode, U1.Pin_1
  N3: D1.anode, U1.Pin_2, DIN1.5
  N4: R2.Pin_0, U1.Pin_6
  N5: R2.Pin_1, U1.Pin_4, Arduino1.GND
  N6: R3.Pin_0, U1.Pin_5, Arduino1.D0RX
  N7: R3.Pin_1, Arduino1.+5V
