# Fritzing sketch id2594_Board_0 (saved by Fritzing 0.9.3b)
stripboards: 1

parts:
  Part1 = Arduino Mega 2560 (Rev3)
  R1 = Resistor [tolerance=±5% resistance=1M package=THT]
  R2 = Resistor [tolerance=±5% resistance=1M package=THT]  # not connected
  R3 = Resistor [tolerance=±5% resistance=1M package=THT]  # not connected
  R4 = Resistor [tolerance=±5% resistance=1M package=THT]  # not connected
  R5 = Resistor [tolerance=±5% resistance=1M package=THT]  # not connected
  R6 = Resistor [tolerance=±5% resistance=1M package=THT]  # not connected
  R7 = Resistor [tolerance=±5% resistance=1M package=THT]  # not connected
  R8 = Resistor [tolerance=±5% resistance=1M package=THT]
  J2 = Piezo Speaker
  J3 = Piezo Speaker  # not connected
  J4 = Piezo Speaker
  J5 = Piezo Speaker
  J6 = Piezo Speaker
  J7 = Piezo Speaker  # not connected
  J8 = Piezo Speaker  # not connected
  J9 = Piezo Speaker  # not connected
  J1 = female pin header, 10 pins [form="♀ (female)"]
  J10 = female pin header, 7 pins [form="♀ (female)"]

nets:
  N1: Part1.A8, R1.Pin_0, J6.pin1, J1.pin10
  N2: Part1.A9, J10.pin7
  N3: Part1.A10, J10.pin6
  N4: Part1.A11, J10.pin5
  N5: Part1.A12, J10.pin4
  N6: Part1.A13, Part1.A1, J2.pin2, J1.pin3, J10.pin3
  N7: Part1.A14, J10.pin2
  N8: Part1.A15, J10.pin1
  N9: Part1.A0, J1.pin2
  N10: Part1.A2, J4.pin1, J1.pin4
  N11: Part1.A3, J1.pin5
  N12: Part1.A4, J6.pin2, J1.pin6
  N13: Part1.A5, J2.pin1, J1.pin7
  N14: Part1.A6, J1.pin8
  N15: Part1.A7, R8.Pin_0, J1.pin9
  N16: Part1.GND, J5.pin2, J1.pin1
