# Fritzing sketch id2595_MIDI_THRU_BOX_0 (saved by Fritzing 0.9.2b)
circuit board: 9.4217cm x 4.71704cm
breadboards: 1

parts:
  MIDI_THRU_A = DIN-5 jack (MIDI) [package=THT]
  MIDI_THRU_B = DIN-5 jack (MIDI) [package=THT]
  MIDI_THRU_C = DIN-5 jack (MIDI) [package=THT]
  MIDI_THRU_D = DIN-5 jack (MIDI) [package=THT]
  R8 = Resistor [tolerance=±5% resistance=220 package=THT]
  1N4148 = Schottky Diode [part_number=1N4148 package="300 mil [THT]"]
  MIDI_IN = DIN-5 jack (MIDI) [package=THT]
  6N138 = IC, DIP package, 8 pins [chip_label=IC]
  R9 = Resistor [tolerance=±5% resistance=220 package=THT]
  R10 = Resistor [tolerance=±5% resistance=220 package=THT]
  R11 = Resistor [tolerance=±5% resistance=220 package=THT]
  7414 = SN74LS14N [package="DIP14 [THT]"]
  Power_plug2 = Power plug
  7805 = Voltage Regulator - 5V [package="TO220 [THT]"]
  10uF = Electrolytic Capacitor [capacitance=10µF package="100 mil [THT, electrolytic]"]
  1N4007 = Rectifier Diode [part_number=1N4001 package="300 mil [THT]"]
  R12 = Resistor [tolerance=±5% resistance=220 package=THT]
  R13 = Resistor [tolerance=±5% resistance=220 package=THT]
  R14 = Resistor [tolerance=±5% resistance=220 package=THT]
  R15 = Resistor [tolerance=±5% resistance=220 package=THT]
  R16 = Resistor [tolerance=±5% resistance=220 package=THT]
  R17 = Resistor [tolerance=±5% resistance=220 package=THT]
  MIDI_THRU_E = DIN-5 jack (MIDI) [package=THT]
  R18 = Resistor [tolerance=±5% resistance=220 package=THT]
  R19 = Resistor [tolerance=±5% resistance=220 package=THT]
  LED = LED - 3mm [color="Red (633nm)" package="3 mm [THT]"]
  R20 = Resistor [tolerance=±5% resistance=220 package=THT]
  0_1uF = Ceramic Capacitor [capacitance=100nF package="100 mil [THT, multilayer]"]

nets:
  N1: MIDI_THRU_A.5, R10.Pin_0
  GND: MIDI_THRU_A.2, MIDI_THRU_B.2, MIDI_THRU_C.2, MIDI_THRU_D.2, 6N138.pin5, 7414.GND, Power_plug2.GND, 7805.GND, 10uF.-, MIDI_THRU_E.2, LED.cathode, 0_1uF.1
  N2: MIDI_THRU_A.4, R11.Pin_0
  N3: MIDI_THRU_B.5, R12.Pin_0
  N4: MIDI_THRU_B.4, R15.Pin_1
  N5: MIDI_THRU_C.5, R13.Pin_0
  N6: MIDI_THRU_C.4, R14.Pin_1
  N7: MIDI_THRU_D.5, R16.Pin_0
  N8: MIDI_THRU_D.4, R17.Pin_1
  N9: R8.Pin_0, 6N138.pin8, R11.Pin_1, 7414.VCC, 7805.output_voltage, R14.Pin_0, R15.Pin_0, R17.Pin_0, R19.Pin_0, R20.Pin_1, 0_1uF.0
  N10: R8.Pin_1, 6N138.pin6, 7414.1A
  N11: 1N4148.cathode, 6N138.pin2, R9.Pin_1
  N12: 1N4148.anode, MIDI_IN.5, 6N138.pin3
  N13: MIDI_IN.4, R9.Pin_0
  N14: R10.Pin_1, 7414.2Y
  N15: 7414.1Y, 7414.2A, 7414.3A, 7414.4A, 7414.5A, 7414.6A
  N16: 7414.3Y, R12.Pin_1
  N17: 7414.4Y, R18.Pin_1
  N18: 7414.5Y, R16.Pin_1
  N19: 7414.6Y, R13.Pin_1
  N20: Power_plug2.VCC, 1N4007.anode
  N21: 7805.input_voltage, 10uF.+, 1N4007.cathode
  N22: MIDI_THRU_E.5, R18.Pin_0
  N23: MIDI_THRU_E.4, R19.Pin_1
  N24: LED.anode, R20.Pin_0

notes:
  THRU D
  THRU C
  THRU B
  THRU A
  THRU E
  IN
  MIDI THRU BOX
  9/12V
  +•)-
  6N138
  MIDI THRU BOX, LABORATORIO DE JUGUETE
