# Fritzing sketch id2596_DIY_Midi_Controller_Triplex_Fzz_0 (saved by Fritzing 0.9.3b)
breadboards: 1

parts:
  R1 = Rotary Potentiometer (Small) [maximum_resistance=100kΩ package=THT]
  R2 = Rotary Potentiometer (Small) [maximum_resistance=100kΩ package=THT]
  R3 = Rotary Potentiometer (Small) [maximum_resistance=100kΩ package=THT]
  S1 = Pushbutton [package="[THT]"]
  S2 = Pushbutton [package="[THT]"]
  S3 = Pushbutton [package="[THT]"]
  hc-sr1 = hc-sr04
  Bauteil1 = Arduino Nano (Rev3.0)
  R4 = Resistor [tolerance=±5% resistance=220 package=THT]
  R5 = Resistor [tolerance=±5% resistance=220 package=THT]
  R6 = Resistor [tolerance=±5% resistance=220 package=THT]

nets:
  VCC: R1.leg1, R2.leg1, R3.leg1, S1.Pin_1, S1.Pin_2, S2.Pin_1, S2.Pin_2, S3.Pin_1, S3.Pin_2, hc-sr1.VCC, Bauteil1.5V
  GND: R1.leg2, R2.leg2, R3.leg2, hc-sr1.GND, Bauteil1.GND, R4.Pin_1, R5.Pin_1, R6.Pin_1
  N1: S1.Pin_3, S1.Pin_4, Bauteil1.D4, R5.Pin_0
  N2: S2.Pin_3, S2.Pin_4, Bauteil1.D2, R6.Pin_0
  N3: S3.Pin_3, S3.Pin_4, Bauteil1.D3, R4.Pin_0
  N4: hc-sr1.Trig, Bauteil1.D9
  N5: hc-sr1.Echo, Bauteil1.D10

notes:
  USB to Midi Adapter Device- USB Powered
