# Fritzing sketch id2599_mignon_powered_duo_led_0 (saved by Fritzing 0.9.3b)
stripboards: 1

parts:
  R3 = Rotary Potentiometer (Small) [maximum_resistance=2.2kΩ package=THT]
  L3 = Inductor [package="400 mil [THT]"]
  R4 = Resistor [tolerance=±5% resistance=220 package=THT]
  L4 = Inductor [package="400 mil [THT]"]
  V3 = DC Power [voltage=1.5V]
  NPN1 = NPN-Transistor [package="TO92 [THT]"]
  LED3 = smd LED [color="Red (633nm)" package="0805 [SMD]"]
  LED4 = LED - 5mm [color="Blue (430nm)" package="5 mm [THT]"]

nets:
  N1: R3.leg1, LED4.anode
  N2: R3.wiper, L3.pin_0, NPN1.C
  N3: R3.leg2, LED3.anode
  N4: L3.pin_1, L4.pin_1, V3.V+
  N5: R4.Pin_0, L4.pin_0
  N6: R4.Pin_1, NPN1.B
  N7: V3.V-, NPN1.E, LED3.cathode, LED4.cathode

notes:
  C
  E
  Mignon powered Duo LED
  + (1,1V - 1,5V)
  -
