# Fritzing sketch id259_adVENTure_0 (saved by Fritzing 0.8.7b)
breadboards: 1

parts:
  Part1 = Arduino Uno (Rev3)
  R1 = Resistor [tolerance=±5% resistance=220 package=THT]
  Q1 = NPN-Transistor [package="TO92 [THT]"]
  D1 = Zener Diode [part_number=1N4732A breakdown_voltage=3.6V package="Melf DO-213 AB [SMD]"]
  U1 = Voltage Regulator - 5V [package="TO220 [THT]"]
  R2 = Resistor [tolerance=±5% resistance=220 package=THT]
  R3 = Resistor [tolerance=±5% resistance=220 package=THT]

nets:
  N1: Part1.A3, U1.output_voltage
  N2: Part1.D11_PWM/MOSI, R1.Pin_1
  GND: Part1.GND, U1.GND, R3.Pin_1
  N3: Part1.VIN, Q1.C, D1.cathode
  N4: R1.Pin_0, Q1.B
  N5: Q1.E, D1.anode
  N6: U1.input_voltage, R2.Pin_1, R3.Pin_0

notes:
  Drive "spinner" motor
  V from Windfarm
  GND for Windfarm
  Spinning motor
