# Fritzing sketch id25_10_btn_muxer_V1.0_0 (saved by Fritzing 0.9.2b)
circuit board: 4.87048cm x 3.15565cm
breadboards: 1

parts:
  D1_1 = Diode [package=diode-1n4148]
  D2_2 = Diode [package=diode-1n4148]
  D4_4 = Diode [package=diode-1n4148]
  D8_8 = Diode [package=diode-1n4148]
  D9_8 = Diode [package=diode-1n4148]
  D9_1 = Diode [package=diode-1n4148]
  D10_2 = Diode [package=diode-1n4148]
  D10_8 = Diode [package=diode-1n4148]
  D3_1 = Diode [package=diode-1n4148]
  D3_2 = Diode [package=diode-1n4148]
  D5_4 = Diode [package=diode-1n4148]
  D5_1 = Diode [package=diode-1n4148]
  D6_2 = Diode [package=diode-1n4148]
  D6_4 = Diode [package=diode-1n4148]
  D7_4 = Diode [package=diode-1n4148]
  D7_3 = Diode [package=diode-1n4148]
  J1 = double row male pin header, 20 pins [form="♂ (male)"]
  J2 = male pin header, 5 pins [form="♂ (male)"]

nets:
  N1: D1_1.A, J1.pin1
  N2: D1_1.C, D9_1.C, D3_1.C, D5_1.C, J2.pin2
  N3: D2_2.A, J1.pin2
  N4: D2_2.C, D10_2.C, D3_2.C, D6_2.C, J2.pin3
  N5: D4_4.A, J1.pin4
  N6: D4_4.C, D5_4.C, D6_4.C, D7_4.C, J2.pin4
  N7: D8_8.A, J1.pin8
  N8: D8_8.C, D9_8.C, D10_8.C, J2.pin5
  N9: D9_8.A, D9_1.A, J1.pin9
  N10: D10_2.A, D10_8.A, J1.pin10
  N11: D3_1.A, D3_2.A, D7_3.C, J1.pin3
  N12: D5_4.A, D5_1.A, J1.pin5
  N13: D6_2.A, D6_4.A, J1.pin6
  N14: D7_4.A, D7_3.A, J1.pin7
  N15: J1.pin11, J1.pin12, J1.pin13, J1.pin14, J1.pin15, J1.pin16, J1.pin17, J1.pin18, J1.pin19, J1.pin20, J2.pin1

notes:
  8 4 2 1 +
  10 9 8 7 6 5 4 3 2 1
  +
  10 Button Muxer V1.0
  by DMA
  GPIOs
  binary
  Buttons
