# Fritzing sketch id2600_Mimic_Arduino_Mega_0 (saved by Fritzing 0.9.2b)

parts:
  Componente4 = Arduino Mega 2560 (Rev3)
  R11 = Rotary Potentiometer (Small) [maximum_resistance=1kΩ package=THT]
  R12 = Rotary Potentiometer (Small) [maximum_resistance=1kΩ package=THT]
  R13 = Rotary Potentiometer (Small) [maximum_resistance=1kΩ package=THT]
  R14 = Rotary Potentiometer (Small) [maximum_resistance=1kΩ package=THT]
  R15 = Rotary Potentiometer (Small) [maximum_resistance=1kΩ package=THT]
  R16 = Rotary Potentiometer (Small) [maximum_resistance=1kΩ package=THT]
  R17 = Rotary Potentiometer (Small) [maximum_resistance=1kΩ package=THT]
  R18 = Rotary Potentiometer (Small) [maximum_resistance=1kΩ package=THT]
  R19 = Rotary Potentiometer (Small) [maximum_resistance=1kΩ package=THT]
  R20 = Rotary Potentiometer (Small) [maximum_resistance=1kΩ package=THT]
  HC-6 = HC-06

nets:
  N1: Componente4.A8, R16.wiper
  N2: Componente4.A9, R11.wiper
  N3: Componente4.A0, R17.wiper
  N4: Componente4.A1, R12.wiper
  N5: Componente4.A2, R20.wiper
  N6: Componente4.A3, R15.wiper
  N7: Componente4.A4, R19.wiper
  N8: Componente4.A5, R14.wiper
  N9: Componente4.A6, R18.wiper
  N10: Componente4.A7, R13.wiper
  N11: Componente4.D17_PWM/RX2, HC-6.connector13
  N12: Componente4.D16_PWM/TX2, HC-6.connector12
  N13: Componente4.GND, R11.leg2, R12.leg2, R13.leg2, R14.leg2, R15.leg2, R16.leg2, R17.leg2, R18.leg2, R19.leg2, R20.leg2, HC-6.connector14
  N14: Componente4.3V3, R11.leg1, R12.leg1, R13.leg1, R14.leg1, R15.leg1, R16.leg1, R18.leg1, R19.leg1, R20.leg1
  N15: Componente4.5V, HC-6.connector15

notes:
  Palmo Dx
  Spalla Sx
  Schiena Sx
  Gomito Sx
  Polso Sx
  Gomito Dx
  Polso Dx
  Palmo Sx
  Spalla Dx
  Schiena Dx
