# Fritzing sketch id2601_Mimic_Arduino_Uno_0 (saved by Fritzing 0.9.2b)

parts:
  R11 = Rotary Potentiometer (Small) [maximum_resistance=1kΩ package=THT]
  R12 = Rotary Potentiometer (Small) [maximum_resistance=1kΩ package=THT]
  R13 = Rotary Potentiometer (Small) [maximum_resistance=1kΩ package=THT]
  R14 = Rotary Potentiometer (Small) [maximum_resistance=1kΩ package=THT]
  R15 = Rotary Potentiometer (Small) [maximum_resistance=1kΩ package=THT]
  R16 = Rotary Potentiometer (Small) [maximum_resistance=1kΩ package=THT]
  R17 = Rotary Potentiometer (Small) [maximum_resistance=1kΩ package=THT]
  R18 = Rotary Potentiometer (Small) [maximum_resistance=1kΩ package=THT]
  R19 = Rotary Potentiometer (Small) [maximum_resistance=1kΩ package=THT]
  R20 = Rotary Potentiometer (Small) [maximum_resistance=1kΩ package=THT]
  HC-6 = HC-06
  MCP1 = MCP3208
  MCP2 = MCP3208
  Componente6 = Arduino Uno (Rev3)

nets:
  N1: R11.leg1, R12.leg1, R13.leg1, R14.leg1, R15.leg1, R16.leg1, R18.leg1, R19.leg1, R20.leg1, MCP1.connector27, MCP2.connector27, Componente6.3V3
  N2: R11.wiper, MCP1.connector17
  N3: R11.leg2, R12.leg2, R13.leg2, R14.leg2, R15.leg2, R16.leg2, R17.leg2, R18.leg2, R19.leg2, R20.leg2, HC-6.connector14, MCP1.connector21, MCP1.connector26, MCP2.connector21, MCP2.connector26, Componente6.GND
  N4: R12.wiper, MCP1.connector13
  N5: R13.wiper, MCP1.connector16
  N6: R14.wiper, MCP1.connector15
  N7: R15.wiper, MCP1.connector14
  N8: R16.wiper, MCP2.connector17
  N9: R17.wiper, MCP2.connector13
  N10: R18.wiper, MCP2.connector16
  N11: R19.wiper, MCP2.connector15
  N12: R20.wiper, MCP2.connector14
  N13: HC-6.connector12, Componente6.D3_PWM
  N14: HC-6.connector13, Componente6.D2
  N15: HC-6.connector15, MCP1.connector28, MCP2.connector28, Componente6.5V
  N16: MCP1.connector22, Componente6.D10_PWM/SS
  N17: MCP1.connector23, MCP2.connector23, Componente6.D11_PWM/MOSI
  N18: MCP1.connector24, MCP2.connector24, Componente6.D12/MISO
  N19: MCP1.connector25, MCP2.connector25, Componente6.D13/SCK
  N20: MCP2.connector22, Componente6.D9_PWM

notes:
  Palmo Dx
  Spalla Sx
  Schiena Sx
  Gomito Sx
  Polso Sx
  Gomito Dx
  Polso Dx
  Palmo Sx
  Spalla Dx
  Schiena Dx
