# Fritzing sketch id2602_Mimic_Nucleo_F401RE_0 (saved by Fritzing 0.9.2b)

parts:
  R1 = Rotary Potentiometer (Small) [maximum_resistance=1kΩ package=THT]
  R2 = Rotary Potentiometer (Small) [maximum_resistance=1kΩ package=THT]
  R3 = Rotary Potentiometer (Small) [maximum_resistance=1kΩ package=THT]
  R4 = Rotary Potentiometer (Small) [maximum_resistance=1kΩ package=THT]
  R5 = Rotary Potentiometer (Small) [maximum_resistance=1kΩ package=THT]
  R6 = Rotary Potentiometer (Small) [maximum_resistance=1kΩ package=THT]
  R8 = Rotary Potentiometer (Small) [maximum_resistance=1kΩ package=THT]
  R9 = Rotary Potentiometer (Small) [maximum_resistance=1kΩ package=THT]
  R10 = Rotary Potentiometer (Small) [maximum_resistance=1kΩ package=THT]
  J1 = STM32 Nucleo boards
  R7 = Rotary Potentiometer (Small) [maximum_resistance=1kΩ package=THT]
  HC-05 = HC-06

nets:
  N1: R1.leg1, R2.leg1, R3.leg1, R4.leg1, R5.leg1, R6.leg1, R8.leg1, R9.leg1, R10.leg1, J1.3V3, R7.leg1
  N2: R1.wiper, J1.A3
  N3: R1.leg2, R2.leg2, R3.leg2, R4.leg2, R5.leg2, R6.leg2, R8.leg2, R9.leg2, R10.leg2, J1.GND#1188, R7.leg2
  N4: R2.wiper, J1.A5/SCL
  N5: R3.wiper, J1.PA7
  N6: R4.wiper, J1.PC4
  N7: R5.wiper, J1.A1
  N8: R6.wiper, J1.PC3
  N9: R8.wiper, J1.PA6
  N10: R9.wiper, J1.A4/SDA
  N11: R10.wiper, J1.A2
  N12: J1.A0, R7.wiper
  N13: J1.D8, J1.D2, HC-05.connector12, HC-05.connector13
  N14: J1.GND#1157, HC-05.connector14
  N15: J1.5V, HC-05.connector15

notes:
  Palmo Dx
  Polso Dx
  Gomito Dx
  Spalla Dx
  Schiena Dx
  Palmo Sx
  Gomito Sx
  Spalla Sx
  Polso Sx
  Schiena Sx
  RX
  TX
  GND
  VCC
