# Fritzing sketch id2606_Christmas_Light_0 (saved by Fritzing 0.9.2b)
breadboards: 1

parts:
  Part1 = Arduino Uno (Rev3)
  R1 = Resistor [tolerance=±5% resistance=220 package=THT]
  R2 = Resistor [tolerance=±5% resistance=220 package=THT]
  R3 = Resistor [tolerance=±5% resistance=10k package=THT]
  LED1 = LED - 5mm [color="Red (633nm)" package="5 mm [THT]"]
  LED2 = LED - 5mm [color="Blue (470nm)" package="5 mm [THT]"]
  LED3 = LED - 5mm [color="Blue (470nm)" package="5 mm [THT]"]  # not connected

nets:
  N1: Part1.GND, R3.Pin_1
  N2: R1.Pin_1, LED1.cathode
  N3: R2.Pin_1, LED2.cathode
  N4: R3.Pin_0, LED1.anode
