# Fritzing sketch id2607_RPI_MiniITX_PCB_0 (saved by Fritzing 0.9.2b)
circuit board: 16.6cm x 17cm
breadboards: 1

parts:
  J1 = ATX24 Pin Power Supply Connector [package=atx24_right_angle]
  SUPPLY_PWR = double row female pin header, 2 pins [form="♀ (female)"]
  J7 = female pin header, 4 pins [form="♀ (female)"]
  Jumper1 = double row female pin header, 4 pins [form="♀ (female)"]
  ext_Eth = RJ45 Jack [package=rj45-8]
  int_Eth = RJ45 Jack [package=rj45-8]
  App_Port1 = RJ45 Jack [package=rj45-8]
  J9 = double row male pin header, 8 pins [form="♂ (male)"]
  App_Port2 = RJ45 Jack [package=rj45-8]
  J10 = double row male pin header, 8 pins [form="♂ (male)"]
  PWR_OK_LED = LED - 5mm [color="Red (633nm)" package="5 mm [THT]"]
  R1 = Resistor [tolerance=±5% resistance=220 package=THT]
  Q1 = NPN-Transistor [package="TO92 [THT]"]
  J14 = female pin header, 17 pins [form="♀ (female)"]
  J15 = rounded female pin header, 4 pins [form="♀ (female rounded)"]
  J16 = rounded female pin header, 4 pins [form="♀ (female rounded)"]
  J17 = rounded female pin header, 2 pins [form="♀ (female rounded)"]
  J18 = rounded female pin header, 2 pins [form="♀ (female rounded)"]
  J19 = rounded female pin header, 4 pins [form="♀ (female rounded)"]
  J20 = rounded female pin header, 4 pins [form="♀ (female rounded)"]
  J21 = rounded female pin header, 2 pins [form="♀ (female rounded)"]
  J22 = rounded female pin header, 2 pins [form="♀ (female rounded)"]
  J25 = female pin header, 2 pins [form="♀ (female)"]
  J27 = female pin header, 2 pins [form="♀ (female)"]
  J26 = female pin header, 2 pins [form="♀ (female)"]  # not connected
  J24 = female pin header, 2 pins [form="♀ (female)"]  # not connected
  J13 = female pin header, 12 pins [form="♀ (female)"]
  LED1 = LED - 5mm [color="Red (633nm)" package="5 mm [THT]"]
  R2 = Resistor [tolerance=±5% resistance=220 package=THT]
  USB1 = USB+SHIELD [package=usb-b-pth]
  J2 = Power Jack [package=power_jack_pth_lock]

nets:
  N1: J1.3.3V, J14.pin1, J14.pin3, J14.pin16, J13.pin1
  GND: J1.GND, PWR_OK_LED.cathode, J14.pin2, J14.pin4, J14.pin6, J14.pin8, J14.pin10, J14.pin12, J14.pin14, J14.pin17, J25.pin1, J25.pin2, J13.pin2, J13.pin3, J13.pin5, J13.pin6, J13.pin7, J13.pin8, J13.pin12, LED1.cathode, USB1.P$1, USB1.GND
  N2: J1.5V, Jumper1.pin4, Q1.E, J14.pin5, J14.pin7, J27.pin1, J27.pin2, J13.pin9, J13.pin10, J13.pin11, R2.Pin_0
  N3: J1.PWR_OK, Q1.C, J14.pin9
  N4: J1.5V_STDBY, J14.pin11
  N5: J1.12V, J14.pin13, J14.pin15
  N6: J1.PS_ON, J13.pin4
  N7: SUPPLY_PWR.pin1, J2.GND, J2.GNDBREAK
  N8: SUPPLY_PWR.pin2, J2.PWR
  N9: J7.pin1, Jumper1.pin1, Jumper1.pin2
  N10: J7.pin2, USB1.D-
  N11: J7.pin3, USB1.D+
  N12: J7.pin4, USB1.P$2
  N13: Jumper1.pin3, USB1.VBUS
  N14: ext_Eth.1, int_Eth.1
  N15: ext_Eth.2, int_Eth.2
  N16: ext_Eth.3, int_Eth.3
  N17: ext_Eth.4, int_Eth.4
  N18: ext_Eth.5, int_Eth.5
  N19: ext_Eth.6, int_Eth.6
  N20: ext_Eth.7, int_Eth.7
  N21: ext_Eth.8, int_Eth.8
  N22: App_Port1.1, J9.pin1
  N23: App_Port1.2, J9.pin2
  N24: App_Port1.3, J9.pin3
  N25: App_Port1.4, J9.pin4
  N26: App_Port1.5, J9.pin5
  N27: App_Port1.6, J9.pin6
  N28: App_Port1.7, J9.pin7
  N29: App_Port1.8, J9.pin8
  N30: App_Port2.1, J10.pin1
  N31: App_Port2.2, J10.pin2
  N32: App_Port2.3, J10.pin3
  N33: App_Port2.4, J10.pin4
  N34: App_Port2.5, J10.pin5
  N35: App_Port2.6, J10.pin6
  N36: App_Port2.7, J10.pin7
  N37: App_Port2.8, J10.pin8
  N38: PWR_OK_LED.anode, R1.Pin_1
  N39: R1.Pin_0, Q1.B
  N40: J15.pin1, J19.pin1
  N41: J15.pin2, J19.pin2
  N42: J15.pin3, J19.pin3
  N43: J15.pin4, J19.pin4
  N44: J16.pin1, J20.pin1
  N45: J16.pin2, J20.pin2
  N46: J16.pin3, J20.pin3
  N47: J16.pin4, J20.pin4
  N48: J17.pin1, J21.pin1
  N49: J17.pin2, J21.pin2
  N50: J18.pin1, J22.pin1
  N51: J18.pin2, J22.pin2
  N52: LED1.anode, R2.Pin_1

notes:
  5V_STBY
  GND
  Vbus
  D-
  D+
  3.3V
  12V
  Raspberry Pi Zero
  Raspberry Pi
  1
  4
  5
  8
  5V_USB
  5V_PWR_SPL
  0V:instable
  5V:stable
  PWR_OK
  5V
  PS_ON
  2xUSB PWR
