# Fritzing sketch id2608_JixMini_0_2_0 (saved by Fritzing 0.9.0b)
circuit board: 13.1cm x 2.73cm
breadboards: 1

parts:
  +5V_Sig_Gnd = male pin header, 3 pins [form="♂ (male)"]
  L1 = SMD_RGB_LED_WS2812B
  C1 = Ceramic Capacitor [capacitance=100nF voltage=10V package="0805 [SMD, multilayer]"]
  C2 = Ceramic Capacitor [capacitance=100nF voltage=10V package="0805 [SMD, multilayer]"]
  L2 = SMD_RGB_LED_WS2812B
  C3 = Ceramic Capacitor [capacitance=100nF voltage=10V package="0805 [SMD, multilayer]"]
  L3 = SMD_RGB_LED_WS2812B
  C4 = Ceramic Capacitor [capacitance=100nF voltage=10V package="0805 [SMD, multilayer]"]
  C6 = Ceramic Capacitor [capacitance=100nF voltage=10V package="0805 [SMD, multilayer]"]
  C5 = Ceramic Capacitor [capacitance=100nF voltage=10V package="0805 [SMD, multilayer]"]
  L4 = SMD_RGB_LED_WS2812B
  L6 = SMD_RGB_LED_WS2812B
  L5 = SMD_RGB_LED_WS2812B
  C7 = Ceramic Capacitor [capacitance=100nF voltage=10V package="0805 [SMD, multilayer]"]
  C8 = Ceramic Capacitor [capacitance=100nF voltage=10V package="0805 [SMD, multilayer]"]
  C9 = Ceramic Capacitor [capacitance=100nF voltage=10V package="0805 [SMD, multilayer]"]
  L8 = SMD_RGB_LED_WS2812B
  L9 = SMD_RGB_LED_WS2812B
  L7 = SMD_RGB_LED_WS2812B
  C10 = Ceramic Capacitor [capacitance=100nF voltage=10V package="0805 [SMD, multilayer]"]
  C13 = Ceramic Capacitor [capacitance=100nF voltage=10V package="0805 [SMD, multilayer]"]
  C14 = Ceramic Capacitor [capacitance=100nF voltage=10V package="0805 [SMD, multilayer]"]
  C11 = Ceramic Capacitor [capacitance=100nF voltage=10V package="0805 [SMD, multilayer]"]
  C15 = Ceramic Capacitor [capacitance=100nF voltage=10V package="0805 [SMD, multilayer]"]
  C12 = Ceramic Capacitor [capacitance=100nF voltage=10V package="0805 [SMD, multilayer]"]
  L10 = SMD_RGB_LED_WS2812B
  L11 = SMD_RGB_LED_WS2812B
  L15 = SMD_RGB_LED_WS2812B
  L12 = SMD_RGB_LED_WS2812B
  L14 = SMD_RGB_LED_WS2812B
  L13 = SMD_RGB_LED_WS2812B
  C16 = Ceramic Capacitor [capacitance=100nF voltage=10V package="0805 [SMD, multilayer]"]
  C28 = Ceramic Capacitor [capacitance=100nF voltage=10V package="0805 [SMD, multilayer]"]
  C29 = Ceramic Capacitor [capacitance=100nF voltage=10V package="0805 [SMD, multilayer]"]
  C25 = Ceramic Capacitor [capacitance=100nF voltage=10V package="0805 [SMD, multilayer]"]
  C22 = Ceramic Capacitor [capacitance=100nF voltage=10V package="0805 [SMD, multilayer]"]
  C20 = Ceramic Capacitor [capacitance=100nF voltage=10V package="0805 [SMD, multilayer]"]
  C21 = Ceramic Capacitor [capacitance=100nF voltage=10V package="0805 [SMD, multilayer]"]
  C30 = Ceramic Capacitor [capacitance=100nF voltage=10V package="0805 [SMD, multilayer]"]
  C23 = Ceramic Capacitor [capacitance=100nF voltage=10V package="0805 [SMD, multilayer]"]
  C17 = Ceramic Capacitor [capacitance=100nF voltage=10V package="0805 [SMD, multilayer]"]
  C19 = Ceramic Capacitor [capacitance=100nF voltage=10V package="0805 [SMD, multilayer]"]
  C26 = Ceramic Capacitor [capacitance=100nF voltage=10V package="0805 [SMD, multilayer]"]
  C27 = Ceramic Capacitor [capacitance=100nF voltage=10V package="0805 [SMD, multilayer]"]
  C18 = Ceramic Capacitor [capacitance=100nF voltage=10V package="0805 [SMD, multilayer]"]
  C24 = Ceramic Capacitor [capacitance=100nF voltage=10V package="0805 [SMD, multilayer]"]
  L16 = SMD_RGB_LED_WS2812B
  L17 = SMD_RGB_LED_WS2812B
  L27 = SMD_RGB_LED_WS2812B
  L20 = SMD_RGB_LED_WS2812B
  L23 = SMD_RGB_LED_WS2812B
  L21 = SMD_RGB_LED_WS2812B
  L30 = SMD_RGB_LED_WS2812B
  L19 = SMD_RGB_LED_WS2812B
  L26 = SMD_RGB_LED_WS2812B
  L22 = SMD_RGB_LED_WS2812B
  L25 = SMD_RGB_LED_WS2812B
  L18 = SMD_RGB_LED_WS2812B
  L24 = SMD_RGB_LED_WS2812B
  L29 = SMD_RGB_LED_WS2812B
  L28 = SMD_RGB_LED_WS2812B
  C39 = Ceramic Capacitor [capacitance=100nF voltage=10V package="0805 [SMD, multilayer]"]
  C35 = Ceramic Capacitor [capacitance=100nF voltage=10V package="0805 [SMD, multilayer]"]
  C40 = Ceramic Capacitor [capacitance=100nF voltage=10V package="0805 [SMD, multilayer]"]
  C31 = Ceramic Capacitor [capacitance=100nF voltage=10V package="0805 [SMD, multilayer]"]
  C41 = Ceramic Capacitor [capacitance=100nF voltage=10V package="0805 [SMD, multilayer]"]
  C38 = Ceramic Capacitor [capacitance=100nF voltage=10V package="0805 [SMD, multilayer]"]
  C34 = Ceramic Capacitor [capacitance=100nF voltage=10V package="0805 [SMD, multilayer]"]
  C37 = Ceramic Capacitor [capacitance=100nF voltage=10V package="0805 [SMD, multilayer]"]
  C42 = Ceramic Capacitor [capacitance=100nF voltage=10V package="0805 [SMD, multilayer]"]
  C33 = Ceramic Capacitor [capacitance=100nF voltage=10V package="0805 [SMD, multilayer]"]
  C36 = Ceramic Capacitor [capacitance=100nF voltage=10V package="0805 [SMD, multilayer]"]
  C32 = Ceramic Capacitor [capacitance=100nF voltage=10V package="0805 [SMD, multilayer]"]
  L34 = SMD_RGB_LED_WS2812B
  L38 = SMD_RGB_LED_WS2812B
  L36 = SMD_RGB_LED_WS2812B
  L42 = SMD_RGB_LED_WS2812B
  L41 = SMD_RGB_LED_WS2812B
  L40 = SMD_RGB_LED_WS2812B
  L39 = SMD_RGB_LED_WS2812B
  L37 = SMD_RGB_LED_WS2812B
  L32 = SMD_RGB_LED_WS2812B
  L33 = SMD_RGB_LED_WS2812B
  L35 = SMD_RGB_LED_WS2812B
  L31 = SMD_RGB_LED_WS2812B

nets:
  N1: +5V_Sig_Gnd.pin1, L1.connector5, C1.1, C2.1, L2.connector5, C3.1, L3.connector5, C4.1, C6.1, C5.1, L4.connector5, L6.connector5, L5.connector5, C7.1, C8.1, C9.1, L8.connector5, L9.connector5, L7.connector5, C10.1, C13.1, C14.1, C11.1, C15.1, C12.1, L10.connector5, L11.connector5, L15.connector5, L12.connector5, L14.connector5, L13.connector5, C16.1, C28.1, C29.1, C25.1, C22.1, C20.1, C21.1, C30.1, C23.1, C17.1, C19.1, C26.1, C27.1, C18.1, C24.1, L16.connector5, L17.connector5, L27.connector5, L20.connector5, L23.connector5, L21.connector5, L30.connector5, L19.connector5, L26.connector5, L22.connector5, L25.connector5, L18.connector5, L24.connector5, L29.connector5, L28.connector5, C39.1, C35.1, C40.1, C31.1, C41.1, C38.1, C34.1, C37.1, C42.1, C33.1, C36.1, C32.1, L34.connector5, L38.connector5, L36.connector5, L42.connector5, L41.connector5, L40.connector5, L39.connector5, L37.connector5, L32.connector5, L33.connector5, L35.connector5, L31.connector5
  N2: +5V_Sig_Gnd.pin2, L1.connector1
  N3: +5V_Sig_Gnd.pin3, L1.connector4, C1.0, C2.0, L2.connector4, C3.0, L3.connector4, C4.0, C6.0, C5.0, L4.connector4, L6.connector4, L5.connector4, C7.0, C8.0, C9.0, L8.connector4, L9.connector4, L7.connector4, C10.0, C13.0, C14.0, C11.0, C15.0, C12.0, L10.connector4, L11.connector4, L15.connector4, L12.connector4, L14.connector4, L13.connector4, C16.0, C28.0, C29.0, C25.0, C22.0, C20.0, C21.0, C30.0, C23.0, C17.0, C19.0, C26.0, C27.0, C18.0, C24.0, L16.connector4, L17.connector4, L27.connector4, L20.connector4, L23.connector4, L21.connector4, L30.connector4, L19.connector4, L26.connector4, L22.connector4, L25.connector4, L18.connector4, L24.connector4, L29.connector4, L28.connector4, C39.0, C35.0, C40.0, C31.0, C41.0, C38.0, C34.0, C37.0, C42.0, C33.0, C36.0, C32.0, L34.connector4, L38.connector4, L36.connector4, L42.connector4, L41.connector4, L40.connector4, L39.connector4, L37.connector4, L32.connector4, L33.connector4, L35.connector4, L31.connector4
  N4: L1.connector0, L2.connector1
  N5: L2.connector0, L3.connector1
  N6: L3.connector0, L4.connector1
  N7: L4.connector0, L5.connector1
  N8: L6.connector0, L7.connector1
  N9: L6.connector1, L5.connector0
  N10: L8.connector0, L9.connector1
  N11: L8.connector1, L7.connector0
  N12: L9.connector0, L10.connector1
  N13: L10.connector0, L11.connector1
  N14: L11.connector0, L12.connector1
  N15: L15.connector0, L16.connector1
  N16: L15.connector1, L14.connector0
  N17: L12.connector0, L13.connector1
  N18: L14.connector1, L13.connector0
  N19: L16.connector0, L17.connector1
  N20: L17.connector0, L18.connector1
  N21: L27.connector0, L28.connector1
  N22: L27.connector1, L26.connector0
  N23: L20.connector0, L21.connector1
  N24: L20.connector1, L19.connector0
  N25: L23.connector0, L24.connector1
  N26: L23.connector1, L22.connector0
  N27: L21.connector0, L22.connector1
  N28: L30.connector0, L31.connector1
  N29: L30.connector1, L29.connector0
  N30: L19.connector1, L18.connector0
  N31: L26.connector1, L25.connector0
  N32: L25.connector1, L24.connector0
  N33: L29.connector1, L28.connector0
  N34: L34.connector0, L35.connector1
  N35: L34.connector1, L33.connector0
  N36: L38.connector0, L39.connector1
  N37: L38.connector1, L37.connector0
  N38: L36.connector0, L37.connector1
  N39: L36.connector1, L35.connector0
  N40: L42.connector1, L41.connector0
  N41: L41.connector1, L40.connector0
  N42: L40.connector1, L39.connector0
  N43: L32.connector0, L33.connector1
  N44: L32.connector1, L31.connector0

notes:
  JixClock mini Display V0.2
  Gnd Sig +5v
