# Fritzing sketch id2609_Light_Meter_PCB_0 (saved by Fritzing 0.8.7b)
circuit board: 4.463cm x 4.46215cm
breadboards: 1

parts:
  S1 = Pushbutton [package=THT]
  S3 = Pushbutton [package=THT]
  IC2 = IC, DIP package, 8 pins [chip_label=230R spacing=300mil]
  OLED1 = 128x32_I2C_Monochrome_OLED_Display
  C1 = Capacitor [package=cap-pth-small-kit]
  S2 = Pushbutton [package=THT]
  R1 = Resistor [tolerance=±5% resistance=200 package=THT]
  R2 = Resistor [tolerance=±5% resistance=100 package=THT]
  R3 = Resistor [tolerance=±5% resistance=10 package=THT]

nets:
  N1: S1.leg0, S3.leg1, S2.leg1
  N2: S1.leg1, R2.Pin_1
  N3: S3.leg0, R3.Pin_1
  N4: IC2.pin3, OLED1.connector4, C1.2
  N5: IC2.pin4, IC2.pin5, OLED1.connector5, OLED1.connector6, C1.1, R1.Pin_0, R2.Pin_0, R3.Pin_0
  N6: S2.leg0, R1.Pin_1
