# Fritzing sketch id260_accel_0 (saved by Fritzing 0.9.2b)
breadboards: 1

parts:
  U1 = ADP3300 - High Accuracy 50mA Low Dropout Linear Regulator [part_number=ADP3300]
  C1 = Electrolytic Capacitor [capacitance=47µF package="100 mil [THT, electrolytic]"]
  C2 = Electrolytic Capacitor [capacitance=10µF package="100 mil [THT, electrolytic]"]
  C3 = Ceramic Capacitor [capacitance=100nF package="100 mil [THT, multilayer]"]
  C4 = Ceramic Capacitor [capacitance=100nF package="100 mil [THT, multilayer]"]
  U2 = ADXL327 - Small, Low Power, #-Axis +/-2G Accelerometer [part_number=ADXL327]

nets:
  GND: U1.NC#1, C1.-, C2.-, C3.0, U2.COM
  5V: U1.+INA, U1.NC#5, C1.+
  3.3V: U1.-V, C2.+, U2.VS
  YOUT: C3.1, U2.YOUT
  ZOUT: C4.1, U2.ZOUT

notes:
  Ms. MEMS Schematic, ADXL327 schematic for ADALP2000, v1.0
