# Fritzing sketch id2610_LM386_0 (saved by Fritzing 0.9.3b)
circuit board: 2.52584cm x 3.92225cm
breadboards: 1

parts:
  U1 = LM386 [package=dip08]
  J1 = Screw terminal - 2 pins [package=THT]
  R1 = Rotary Potentiometer (Large) [maximum_resistance=100kΩ package=THT]
  J2 = Screw terminal - 2 pins [package=THT]
  J3 = Screw terminal - 2 pins [package=THT]
  C1 = Electrolytic Capacitor [capacitance=10µF voltage=6.3V package="100 mil [THT, electrolytic]"]
  C2 = Ceramic Capacitor [capacitance=50nF package="100 mil [THT, multilayer]"]
  R2 = Resistor [tolerance=±5% resistance=10 package=THT]
  C3 = Tantalum Capacitor [capacitance=250nF voltage=16V package="100 mil [THT, tantalum]"]

nets:
  N1: U1.GAIN, C1.-, C1.+
  N2: U1.-IN, U1.V-, J1.pin1, R1.leg1, J2.pin1, J3.pin2, R2.Pin_0
  N3: U1.+IN, R1.wiper
  N4: U1.OUT, C2.1, C3.+
  N5: U1.V+, J1.pin2
  N6: R1.leg2, J2.pin2
  N7: J3.pin1, C3.-
  N8: C2.0, R2.Pin_1
