# Fritzing sketch id2612_FuenteVoltaje_0 (saved by Fritzing 0.9.3b)
breadboards: 1

parts:
  C1 = Electrolytic Capacitor [capacitance=1µF package="100 mil [THT, electrolytic]"]
  C2 = Electrolytic Capacitor [capacitance=1µF package="100 mil [THT, electrolytic]"]
  R1 = Rotary Potentiometer (Small) [maximum_resistance=100kΩ package=THT]
  R2 = Resistor [tolerance=±5% resistance=220 package=THT]
  U1 = Voltage Regulator - Variable [package="TO220 [THT]"]
  C3 = Electrolytic Capacitor [capacitance=1µF package="100 mil [THT, electrolytic]"]
  D1 = Rectifier Diode [part_number=1N4001 package="300 mil [THT]"]
  D2 = Rectifier Diode [part_number=1N4001 package="300 mil [THT]"]
  D3 = Rectifier Diode [part_number=1N4001 package="300 mil [THT]"]
  D4 = Rectifier Diode [part_number=1N4001 package="300 mil [THT]"]

nets:
  N1: C1.-, C2.-, R2.Pin_0, U1.OUT
  N2: C1.+, C2.+, R1.wiper, C3.+, D3.anode, D4.anode
  N3: R1.leg2, R2.Pin_1, U1.ADJ
  N4: U1.IN, C3.-, D1.cathode, D2.cathode
  N5: D1.anode, D4.cathode
  N6: D2.anode, D3.cathode
