# Fritzing sketch id2614_MiniBFlipFlop_0 (saved by Fritzing 0.8.7b)
circuit board: 2cm x 2cm
breadboards: 1

parts:
  R1 = Resistor [tolerance=±5% resistance=1k package=THT]
  R2 = Resistor [tolerance=±5% resistance=100k package=THT]
  R3 = Resistor [tolerance=±5% resistance=100k package=THT]
  R4 = Resistor [tolerance=±5% resistance=1k package=THT]
  Q1 = NPN-Transistor [package="TO92 [THT]"]
  Q2 = NPN-Transistor [package="TO92 [THT]"]

nets:
  LED2: R1.Pin_0
  N1: R1.Pin_1, R2.Pin_0, Q2.C
  S1: R2.Pin_1, Q1.B
  S2: R3.Pin_0, Q2.B
  N2: R3.Pin_1, R4.Pin_1, Q1.C
  LED1: R4.Pin_0
  GND: Q1.E, Q2.E

notes:
  BFlipFlop
  DevDiary
  ORG
  R1
  MiniBFlipFlop - Bistabiles FlipFlop -
  S1 - Ein Button zwischen S1 und GND
  S2 - Ein Button zwischen S2 und GND
  LED1 - Eine LED zwischen LED1 und +
  LED2 - Eine LED zwischen LED2 und +
  Betrieb mit einer 9V DC Spannungsquelle. (9V Blockbatterie)
  Für weitere Fragen bitte eine EMail an hq@devdiary.org senden.
