# Fritzing sketch id2615_Motor_Creative_Electronics_motor_0 (saved by Fritzing 0.9.3b)
breadboards: 1

parts:
  R1 = Resistor [tolerance=±5% resistance=220 package=THT]
  S1 = Pushbutton [package="[THT]"]
  Onderdeel1 = Arduino Uno (Rev3)
  Onderdeel2 = EasyDriver_v44
  M1 = Stepper Motor - Bipolar
  VCC1 = Battery block 9V

nets:
  N1: R1.Pin_0, S1.Pin_1, S1.Pin_2, Onderdeel1.D3_PWM
  N2: R1.Pin_1, Onderdeel1.3V3
  N3: S1.Pin_3, S1.Pin_4, Onderdeel2.GND, VCC1.-
  N4: Onderdeel1.D8, Onderdeel2.DIR
  N5: Onderdeel1.D9_PWM, Onderdeel2.STEP
  N6: Onderdeel2.V+, VCC1.+
  N7: Onderdeel2.OUT2A, M1.A
  N8: Onderdeel2.OUT2B, M1.C
  N9: Onderdeel2.OUT1A, M1.B
  N10: Onderdeel2.OUT1B, M1.D
