# Fritzing sketch id2617_retroDuino_0 (saved by Fritzing 0.9.2b)
breadboards: 2

parts:
  Eleman1 = Arduino Uno (Rev3)
  S1 = Pushbutton [package="[THT]"]
  S2 = Pushbutton [package="[THT]"]
  Nokia_5110_LCD_Module1 = Nokia 5110 LCD (8 pin)
  R1 = Resistor [tolerance=±5% resistance=220 package=THT]
  R2 = Resistor [tolerance=±5% resistance=220 package=THT]
  R3 = Resistor [tolerance=±5% resistance=220 package=THT]

nets:
  N1: Eleman1.D8, Nokia_5110_LCD_Module1.connector7
  N2: Eleman1.D9_PWM, Nokia_5110_LCD_Module1.connector0
  N3: Eleman1.D10_PWM/SS, Nokia_5110_LCD_Module1.connector6
  N4: Eleman1.D11_PWM/MOSI, Nokia_5110_LCD_Module1.connector5
  N5: Eleman1.D12/MISO, Nokia_5110_LCD_Module1.connector4
  N6: Eleman1.D2, S2.Pin_1, S2.Pin_2, R2.Pin_0
  N7: Eleman1.D3_PWM, S1.Pin_3, S1.Pin_4, R3.Pin_1
  N8: Eleman1.D7, R1.Pin_0
  N9: Eleman1.3V3, Nokia_5110_LCD_Module1.connector3
  N10: Eleman1.GND, Nokia_5110_LCD_Module1.connector2
  N11: S1.Pin_1, S1.Pin_2, S2.Pin_3, S2.Pin_4
  N12: Nokia_5110_LCD_Module1.connector1, R1.Pin_1
  N13: R2.Pin_1, R3.Pin_0

notes:
  KONTROL KOLU
  EKRAN
