# Fritzing sketch id2618_MiniSumoShieldArduino_0 (saved by Fritzing 0.7.12b)
breadboards: 1

parts:
  J1 = female pin header, 8 pins [form="♀ (female)"]
  J2 = female pin header, 7 pins [form="♀ (female)"]
  R1 = Resistor [tolerance=±5% resistance=1 package=THT]
  R2 = Resistor [tolerance=±5% resistance=1 package=THT]
  M1 = DC Motor
  M2 = DC Motor
  D1 = Rectifier Diode [part_number=1N4935 package="300 mil [THT]"]
  D2 = Rectifier Diode [part_number=1N4935 package="300 mil [THT]"]
  D3 = Rectifier Diode [part_number=1N4935 package="300 mil [THT]"]
  D4 = Rectifier Diode [part_number=1N4935 package="300 mil [THT]"]
  D5 = Rectifier Diode [part_number=1N4935 package="300 mil [THT]"]
  D6 = Rectifier Diode [part_number=1N4935 package="300 mil [THT]"]
  D7 = Rectifier Diode [part_number=1N4935 package="300 mil [THT]"]
  D8 = Rectifier Diode [part_number=1N4935 package="300 mil [THT]"]
  C3 = Ceramic Capacitor [capacitance=100nF package="200 mil [THT, multilayer]"]
  C1 = Ceramic Capacitor [capacitance=100nF voltage=50V package="200 mil [THT, multilayer]"]
  J3 = female pin header, 6 pins [form="♀ (female)"]
  J4 = female pin header, 6 pins [form="♀ (female)"]
  J5 = female pin header, 8 pins [form="♀ (female)"]
  J6 = female pin header, 8 pins [form="♀ (female)"]
  J7 = longpad pin header, 2 pins [form="long pad"]
  R3 = Resistor [tolerance=±5% resistance=330 package=THT]
  J8 = female pin header, 4 pins [form="♀ (female)"]
  J9 = female pin header, 4 pins [form="♀ (female)"]
  R4 = Resistor [tolerance=±5% resistance=330 package=THT]
  R5 = Resistor [tolerance=±5% resistance=10k package=THT]
  R6 = Resistor [tolerance=±5% resistance=10k package=THT]
  Arduino2 = Arduino
  C4 = Electrolytic Capacitor [capacitance=10µF voltage=20V package="100 mil [THT, electrolytic]"]
  U1 = Voltage Regulator - 5V [package="TO220 [THT]"]

nets:
  N1: J1.pin1, R2.Pin_0
  N2: J1.pin2, M1.pin_1, D2.cathode, D4.anode
  N3: J1.pin3, J6.pin3, Arduino2.D10
  N4: J1.pin4, J6.pin2, Arduino2.D9
  N5: J1.pin5, J1.pin6, J2.pin3, J4.pin4, J8.pin3, J8.pin4, J9.pin1, J9.pin2, Arduino2.+5V
  N6: J1.pin7, M2.pin_2, D5.anode, D8.cathode
  N7: J1.pin8, R1.Pin_0
  N8: J2.pin1, M1.pin_2, D1.cathode, D3.anode
  N9: J2.pin2, D3.cathode, D4.cathode, D5.cathode, D7.cathode, C3.1, J7.pin1, U1.input_voltage
  GND: J2.pin4, R1.Pin_1, R2.Pin_1, D1.anode, D2.anode, D6.anode, D8.anode, C3.0, C1.0, J4.pin2, J4.pin3, J6.pin7, J7.pin2, R3.Pin_0, R4.Pin_0, R5.Pin_0, R6.Pin_0, Arduino2.GND, C4.-, U1.GND
  N10: J2.pin5, J5.pin7, Arduino2.D6
  N11: J2.pin6, J5.pin6, Arduino2.D5
  N12: J2.pin7, M2.pin_1, D6.cathode, D7.anode
  N13: C1.1, J4.pin1, Arduino2.VIN, C4.+, U1.output_voltage
  N14: J3.pin1, J8.pin2, R5.Pin_1, Arduino2.A5
  N15: J3.pin2, J9.pin3, R6.Pin_1, Arduino2.A4
  N16: J3.pin3, Arduino2.A3
  N17: J3.pin4, Arduino2.A2
  N18: J3.pin5, Arduino2.A1
  N19: J3.pin6, Arduino2.A0
  N20: J4.pin5, Arduino2.3V3
  N21: J4.pin6, Arduino2.RST
  N22: J5.pin1, Arduino2.D0RX
  N23: J5.pin2, Arduino2.D1TX
  N24: J5.pin3, Arduino2.D2
  N25: J5.pin4, Arduino2.D3
  N26: J5.pin5, Arduino2.D4
  N27: J5.pin8, Arduino2.D7
  N28: J6.pin1, Arduino2.D8
  N29: J6.pin4, Arduino2.D11
  N30: J6.pin5, Arduino2.D12
  N31: J6.pin6, Arduino2.D13
  N32: J6.pin8, Arduino2.aref
  N33: R3.Pin_1, J8.pin1
  N34: J9.pin4, R4.Pin_1

notes:
  sergiofloro
