# Fritzing sketch id2618_led_yakma (saved by Fritzing 0.9.3b)
breadboards: 1

parts:
  LED1 = LED - 5mm [color="Red (633nm)" package="5 mm [THT]"]
  Parça1 = Arduino Uno (Rev3)
  R1 = Resistor [tolerance=±5% resistance=220 package=THT]

nets:
  N1: LED1.cathode, Parça1.GND
  N2: LED1.anode, R1.Pin_0
  N3: Parça1.D2, R1.Pin_1
