# Fritzing sketch id2619_minitel+xbee_v1_0 (saved by Fritzing 0.7.10b)
stripboards: 1

parts:
  DIN1 = DIN-5 jack (MIDI) [package=THT]
  U1 = XBee
  U2 = Voltage Regulator - 5V [package="TO220 [THT]"]

nets:
  N1: DIN1.3, U1.pin3
  N2: DIN1.5, U2.input_voltage
  GND: DIN1.2, U1.GND, U2.GND
  N3: DIN1.1, U1.pin2
  N4: U1.VCC, U2.output_voltage

notes:
  2 masse
  4 entrée PT (non utilisé)
  5 sortie 8,5V
  3 sortie TX
  1 entrée RX
