# Fritzing sketch id2620_AlfPrimero09052016_0 (saved by Fritzing 0.9.2b)
circuit board: 8.46667cm x 5.64444cm
breadboards: 1

parts:
  Parte1 = Arduino Uno (Rev3)
  T1 = LM35 Temperature Sensor [package="TO92 [THT]"]

nets:
  N1: Parte1.A5/SCL, T1.Vout
  GND: Parte1.GND, T1.GND
  N2: Parte1.5V, T1.+Vs

notes:
  Rojo-> Alimentacion;
  Negro-> GND;
  Azul ->Salida.
