# Fritzing sketch id2621_Mister_EagleEyes_0 (saved by Fritzing 0.9.3b)
breadboards: 1

parts:
  hc-sr1 = hc-sr04
  Part1 = Arduino Uno (Rev3) - ICSP
  R1 = Resistor [tolerance=±5% resistance=220 package="0402 [SMD]"]
  R2 = Resistor [tolerance=±5% resistance=220 package="0402 [SMD]"]
  R3 = Resistor [tolerance=±5% resistance=220 package="0402 [SMD]"]
  LED1 = smd LED [color="Green (555nm)" package="1206 [SMD]"]
  LED2 = smd LED [color="Yellow (595nm)" package="1206 [SMD]"]
  LED3 = smd LED [color="Red (633nm)" package="1206 [SMD]"]
  LED4 = LED - 5mm [color="Blue (505nm)" package="5 mm [THT]"]
  R4 = Resistor [tolerance=±5% resistance=220 package=THT]

nets:
  VCC: hc-sr1.VCC, Part1.5V
  N1: hc-sr1.Trig, Part1.D10_PWM/SS
  N2: hc-sr1.Echo, Part1.D11_PWM/MOSI, R4.Pin_1
  GND: hc-sr1.GND, Part1.GND, LED1.anode, LED2.anode, LED3.anode, LED4.anode
  N3: Part1.D4, R1.Pin_0
  N4: Part1.D5_PWM, R2.Pin_0
  N5: Part1.D6_PWM, R3.Pin_0
  N6: R1.Pin_1, LED1.cathode
  N7: R2.Pin_1, LED2.cathode
  N8: R3.Pin_1, LED3.cathode
  N9: LED4.cathode, R4.Pin_0

notes:
  The gren LED will blink when an object is between 50 to 0 cm away, yellow for 35 to 0 and red at 20 to 0
  ---------------------------------------------
  The blue light is not necissary as it just bilnks when a returning ultrasound wave is recieved
