# Fritzing sketch id2623_boomgate_0 (saved by Fritzing 0.6.3b)
breadboards: 1

parts:
  R1 = Resistor [tolerance=±5% resistance=10k package=THT]
  Arduino1 = Arduino
  S1 = Reed switch [package=THT]
  J1 = Basic Servo
  R2 = Resistor [tolerance=±5% resistance=220 package=THT]
  R3 = Resistor [tolerance=±5% resistance=220 package=THT]
  R4 = Resistor [tolerance=±5% resistance=220 package=THT]
  LED1 = LED - 5mm [color="Red (633nm)" package="5 mm [THT]"]
  LED2 = LED - 5mm [color="Red (633nm)" package="5 mm [THT]"]
  LED3 = LED - 5mm [color="Red (633nm)" package="5 mm [THT]"]
  S2 = Pushbutton [package="[THT]"]
  R5 = Resistor [tolerance=±5% resistance=10k package=THT]

nets:
  N1: R1.Pin_0, Arduino1.D3, S1.pin_2, LED3.anode
  GND: R1.Pin_1, Arduino1.GND, J1.gnd, R2.Pin_0, R3.Pin_0, R4.Pin_0, R5.Pin_1
  N2: Arduino1.D5, J1.pulse
  N3: Arduino1.D4, LED1.anode
  +5V: Arduino1.D2, Arduino1.+5V, S1.pin_1, J1.vcc, LED2.anode, S2.Pin_1, S2.Pin_2, S2.Pin_3, S2.Pin_4, R5.Pin_0
  N4: R2.Pin_1, LED1.cathode
  N5: R3.Pin_1, LED2.cathode
  N6: R4.Pin_1, LED3.cathode

notes:
  < Open State
  < Safety
  < Open Request
  To Access Controller Inputs:
  * open state <<<
  * safety state <<<
  To Acceess Controller Ouput:
  * relay (n/o) >>>
  Reed Switch to simulate induction safety loop.
  Servo Motor to control boom
  Switch to allow for testing without being hooked up to the Access Controller
