# Fritzing sketch id2624_Reflex_arc_0 (saved by Fritzing 0.9.2b)
breadboards: 1

parts:
  S1 = Pushbutton [package="[THT]"]
  J1 = Basic Servo
  Part1 = Arduino Uno (Rev3)

nets:
  GND: S1.Pin_1, S1.Pin_2, J1.gnd, Part1.GND
  N1: S1.Pin_3, S1.Pin_4, Part1.D9_PWM
  VCC: J1.vcc, Part1.5V
