# Fritzing sketch id2625_Modelo1_0 (saved by Fritzing 0.9.2b)
breadboards: 1

parts:
  Parte1 = Arduino Leonardo (Rev3b)
  LED1 = LED - 5mm [color="Red (633nm)" package="5 mm [THT]"]
  R1 = Resistor [tolerance=±5% resistance=220 package="1206 [SMD]"]

nets:
  N1: Parte1.GND, LED1.cathode
  N2: Parte1.D13_PWM, R1.Pin_0
  N3: LED1.anode, R1.Pin_1

notes:
  Esta sencilla configuración servirá para hacer varias pruebas con instrucciones como HIGH, LOW y AnalogWrite.
