# Fritzing sketch id2626_Modelo_2_0 (saved by Fritzing 0.9.2b)
breadboards: 1

parts:
  Parte1 = Arduino Leonardo (Rev3b)
  R1 = Resistor [tolerance=±5% resistance=220 package="1206 [SMD]"]
  LED1 = smd LED [color="Red (633nm)" package="1206 [SMD]"]
  LED2 = smd LED [color="Red (633nm)" package="1206 [SMD]"]
  LED3 = smd LED [color="Red (633nm)" package="1206 [SMD]"]
  R2 = Resistor [tolerance=±5% resistance=220 package=THT]
  R3 = Resistor [tolerance=±5% resistance=220 package=THT]

nets:
  N1: Parte1.D0/RX, R3.Pin_0
  N2: Parte1.D7, R2.Pin_0
  N3: Parte1.GND, LED1.cathode, LED2.cathode, LED3.cathode
  N4: Parte1.D13_PWM, R1.Pin_0
  N5: R1.Pin_1, LED1.anode
  N6: LED2.anode, R2.Pin_1
  N7: LED3.anode, R3.Pin_1

notes:
  Modelo 2. Para trabajar con diferentes series, diferentes señales simultáneas y para explicar la diferencia entre pines con y sin PWM.
  Creado por: MTI Raúl David Salomón García
