# Fritzing sketch id2627_Modelo_3_0 (saved by Fritzing 0.9.2b)
breadboards: 1

parts:
  Parte1 = Arduino Leonardo (Rev3b)
  T1 = LM35 Temperature Sensor [package="TO92 [THT]"]
  LED1 = smd LED [color="Red (633nm)" package="0805 [SMD]"]
  LED2 = smd LED [color="Green (555nm)" package="0805 [SMD]"]
  LED3 = smd LED [color="Yellow (592nm)" package="0805 [SMD]"]
  R1 = Resistor [tolerance=±5% resistance=220 package="0603 [SMD]"]
  R2 = Resistor [tolerance=±5% resistance=220 package="0603 [SMD]"]
  R3 = Resistor [tolerance=±5% resistance=220 package="0603 [SMD]"]

nets:
  N1: Parte1.5V, T1.+Vs
  GND: Parte1.GND, T1.GND, LED1.cathode, LED2.cathode, LED3.cathode
  N2: Parte1.A0, T1.Vout
  N3: Parte1.D11_PWM, R1.Pin_0
  N4: Parte1.D12/A11, R2.Pin_0
  N5: Parte1.D13_PWM, R3.Pin_0
  N6: LED1.anode, R1.Pin_1
  N7: LED2.anode, R3.Pin_1
  N8: LED3.anode, R2.Pin_1

notes:
  Modelo 3. Usaremos este modelo para probar el sensor LM35 a traves de la funcion analogRead() y otras que ya se han utilizado. Tambien se vera como funciona el monitor serial que nos permite saber en "tiempo real" el comportamiento de una variable obtenida por un sensor, al mismo tiempo, dependiendo de los valores de esa variable vamos a utilizar los leds como actuadores.
  M.T.I. Raul David Salomon Garcia
