# Fritzing sketch id2628_modem_on_off_0 (saved by Fritzing 0.9.2b)
breadboards: 1

parts:
  S1 = Pushbutton [package="[THT]"]
  U1 = TLP621 [package=THT]
  Part1 = Arduino Uno (Rev3)
  R1 = Resistor [tolerance=±5% resistance=220 package="2512 [SMD]"]

nets:
  N1: S1.Pin_1, S1.Pin_2, U1.Pin_4
  N2: S1.Pin_3, S1.Pin_4, U1.Pin_3
  N3: U1.Pin_1, R1.Pin_1
  N4: U1.Pin_2, Part1.GND
  N5: Part1.A0, R1.Pin_0

notes:
  Button In The Modem
