# Fritzing sketch id2629_Modified_Binary_Counter_112414_0 (saved by Fritzing 0.8.7b)
breadboards: 1

parts:
  Part1 = Arduino Uno (Rev3)
  R1 = Resistor [tolerance=±5% resistance=220 package=THT]
  R2 = Resistor [tolerance=±5% resistance=220 package=THT]
  R3 = Resistor [tolerance=±5% resistance=220 package=THT]
  R4 = Resistor [tolerance=±5% resistance=220 package=THT]
  R5 = Resistor [tolerance=±5% resistance=220 package=THT]
  R6 = Resistor [tolerance=±5% resistance=220 package=THT]
  R7 = Resistor [tolerance=±5% resistance=220 package=THT]
  R8 = Resistor [tolerance=±5% resistance=220 package=THT]
  LED2 = LED - 5mm [color="Red (633nm)" package="5 mm [THT]"]
  LED3 = LED - 5mm [color="Red (633nm)" package="5 mm [THT]"]
  LED4 = LED - 5mm [color="Red (633nm)" package="5 mm [THT]"]
  LED5 = LED - 5mm [color="Red (633nm)" package="5 mm [THT]"]
  LED6 = LED - 5mm [color="Red (633nm)" package="5 mm [THT]"]
  LED7 = LED - 5mm [color="Red (633nm)" package="5 mm [THT]"]
  LED8 = LED - 5mm [color="Red (633nm)" package="5 mm [THT]"]
  LED1 = smd LED [color="Red (633nm)" package="1206 [SMD]"]
  R10 = Resistor [tolerance=±5% resistance=220 package=THT]
  S1 = Pushbutton [package="[THT]"]

nets:
  N1: Part1.D8, LED4.cathode
  N2: Part1.D9_PWM, LED5.cathode
  N3: Part1.D10_PWM/SS, LED6.cathode
  N4: Part1.D11_PWM/MOSI, LED7.cathode
  N5: Part1.D12/MISO, LED8.cathode
  N6: Part1.D2, R10.Pin_0, S1.Pin_1, S1.Pin_2
  N7: Part1.D5_PWM, LED1.cathode
  N8: Part1.D6_PWM, LED2.cathode
  N9: Part1.D7, LED3.cathode
  N10: Part1.5V, R1.Pin_1, R2.Pin_1, R3.Pin_1, R4.Pin_1, R5.Pin_1, R6.Pin_1, R7.Pin_1, R8.Pin_1
  N11: R1.Pin_0, LED1.anode
  N12: R2.Pin_0, LED2.anode
  N13: R3.Pin_0, LED3.anode
  N14: R4.Pin_0, LED4.anode
  N15: R5.Pin_0, LED7.anode
  N16: R6.Pin_0, LED5.anode
  N17: R7.Pin_0, LED6.anode
  N18: R8.Pin_0, LED8.anode
  N19: S1.Pin_3, S1.Pin_4
