# Fritzing sketch id262_ADXL345_2_0 (saved by Fritzing 0.7.4b)
breadboards: 1

parts:
  R1 = Resistor [tolerance=±5% resistance=10k package=THT]
  R2 = Resistor [tolerance=±5% resistance=10k package=THT]
  Part4 = Triple Axis Accelerometer Breakout - ADXL345
  Arduino1 = Arduino

nets:
  VCC: R1.Pin_0, R2.Pin_0, Part4.VCC, Part4.CS, Arduino1.3V3
  N1: R1.Pin_1, Part4.SDA, Arduino1.A4
  N2: R2.Pin_1, Part4.SCL, Arduino1.A5
  GND: Part4.GND, Part4.SDO, Arduino1.GND
