# Fritzing sketch id2631_Micro_M+_comp_014_1_0 (saved by Fritzing 0.9.1b)
circuit board: 9.9cm x 4.9cm
stripboards: 1

parts:
  C83 = Ceramic Capacitor [capacitance=100nF voltage=20V package="100 mil [THT, multilayer]"]
  R15 = Resistor [tolerance=±5% resistance=100k package=THT]
  R9915 = Resistor [tolerance=±5% resistance=100 package=THT]
  U2 = 555 Timer [package="DIP8 [THT]"]
  U1 = LM 358 Dual Op-Amp [part_number=LM2903 package="DIP8 [THT]"]
  R9 = Resistor [tolerance=±5% resistance=100k package=THT]
  C5 = Ceramic Capacitor [capacitance=100nF voltage=20V package="100 mil [THT, multilayer]"]
  C3 = Ceramic Capacitor [capacitance=10nF voltage=20V package="100 mil [THT, multilayer]"]
  R8 = Resistor [tolerance=±5% resistance=10k package=THT]
  R13 = Resistor [tolerance=±5% resistance=10k package=THT]
  D4 = Rectifier Diode [part_number=80SQ045 package="300 mil [THT]"]
  IC1 = Voltage Regulator [package=to-92]
  D3 = Rectifier Diode [part_number=1N4002 package="300 mil [THT]"]
  Q3 = 2N7000
  Q1 = 2N7000
  C82 = Ceramic Capacitor [capacitance=100nF voltage=20V package="100 mil [THT, multilayer]"]
  R9910 = Resistor [tolerance=±5% resistance=100k package=THT]
  R4 = Resistor [tolerance=±5% resistance=1M package=THT]
  R7 = Resistor [tolerance=±5% resistance=10k package=THT]
  R3 = Resistor [tolerance=±5% resistance=2k package=THT]
  U4 = Zener Diode [part_number=1N4732A breakdown_voltage=5.1V package="300 mil [THT]"]
  R6 = Resistor [tolerance=±5% resistance=1.8k package=THT]
  R5 = Resistor [tolerance=±5% resistance=10k package=THT]
  D1 = Schottky Diode [part_number=1N914 package="300 mil [THT]"]
  R16 = Resistor [tolerance=±5% resistance=100k package=THT]
  J2 = Screw terminal - 2 pins [package=THT]
  J1 = Screw terminal - 2 pins [package=THT]
  Q4 = Basic FET P-Channel [part_number=IRF4905 package="TO220 [THT]"]
  R1 = Resistor [tolerance=±5% resistance=100k package=THT]
  C4 = Electrolytic Capacitor [capacitance=22µF voltage=20V package="100 mil [THT, electrolytic]"]
  R2 = POT [package=3362u]
  C2 = Electrolytic Capacitor [capacitance=22µF voltage=20V package="100 mil [THT, electrolytic]"]
  C6 = Electrolytic Capacitor [capacitance=22µF voltage=20V package="100 mil [THT, electrolytic]"]
  C8 = Ceramic Capacitor [capacitance=100nF package="100 mil [THT, multilayer]"]
  C1 = Ceramic Capacitor [capacitance=100nF package="100 mil [THT, multilayer]"]
  R12 = Resistor [tolerance=±5% resistance=27k package=THT]
  D2 = Zener Diode [part_number=1N4747 breakdown_voltage=20V package="300 mil [THT]"]
  LED2 = LEDs [package=led10mm]
  R9910_2 = Resistor [tolerance=±5% resistance=5k package=THT]
  R14 = Resistor [tolerance=±5% resistance=68 package=THT]
  LED3 = LEDs [package=led10mm]
  R10 = Resistor [tolerance=±5% resistance=5k package=THT]
  Q5 = 2N7000

nets:
  GND: C83.0, U2.Ground, U1.connector3, R9.Pin_1, C3.1, IC1.IN, Q3.connector0, Q1.connector0, C82.0, R3.Pin_1, U4.anode, D1.anode, J2.pin2, J1.pin2, C4.-, C2.-, C6.+, C8.1, C1.0, Q5.connector0
  8V/V+: C83.1, R15.Pin_0, U2.Reset, U2.Vcc_Supply_Voltage, U1.connector7, IC1.GND, C82.1, R9910.Pin_1, R6.Pin_1, R16.Pin_0, C6.-, R9910_2.Pin_1
  N1: R15.Pin_1, R9915.Pin_1, U2.Discharge
  N2: R9915.Pin_0, U2.Threshold, C2.+
  N3: U2.Trigger, C5.1, R16.Pin_1
  N4: U2.Output, Q3.connector1
  N5: U2.Control_Voltage, C3.0
  N6: U1.connector0, C5.0, R8.Pin_1, R9910.Pin_0, R4.Pin_1
  input-: U1.connector1, R5.Pin_1, D1.cathode, C1.1
  N7: U1.connector2, R4.Pin_0, R7.Pin_1
  VBatt: U1.connector4, D4.cathode, J2.pin1, R1.Pin_1
  N8: U1.connector6, LED2.C
  gate1: R9.Pin_0, R8.Pin_0, Q3.connector2, Q1.connector1, Q5.connector1
  N9: R13.Pin_0, Q4.gate
  N10: R13.Pin_1, R12.Pin_0, D2.anode, R14.Pin_0
  N11: D4.anode, Q4.drain
  Vreg_in: IC1.OUT, D3.cathode, C8.0, R10.Pin_0
  PV+: D3.anode, J1.pin1, Q4.source, R12.Pin_1, D2.cathode
  N12: Q1.connector2, R14.Pin_1
  N13: R7.Pin_0, U4.cathode, R6.Pin_0, C4.+
  N14: R3.Pin_0, R2.E
  N15: R5.Pin_0, R2.S
  N16: R1.Pin_0, R2.A
  N17: LED2.A, R9910_2.Pin_0
  N18: LED3.A, R10.Pin_1
  N19: LED3.C, Q5.connector2

notes:
  LM385 part is used as a pin compatible comparator LM193, LM2903, LM293, LM393.
  The Voltage regulator is used instead of an LM78L08 and are NOT pin compatible.
  Stripboard fr Kjell & Co har 38 banor & ca 62 hål per bana.
