# Fritzing sketch id2632_Micro_M+_comp_023_0 (saved by Fritzing 0.9.1b)
circuit board: 10.2634cm x 5.38311cm
stripboards: 1

parts:
  C83 = Ceramic Capacitor [capacitance=100nF voltage=20V package="100 mil [THT, multilayer]"]
  R15 = Resistor [tolerance=±5% resistance=120k package=THT]
  R50 = Resistor [tolerance=±5% resistance=82 package=THT]
  U2 = 555 Timer [package="DIP8 [THT]"]
  U1 = LM 358 Dual Op-Amp [part_number=LM2903 package="DIP8 [THT]"]
  C3 = Ceramic Capacitor [capacitance=10nF voltage=20V package="100 mil [THT, multilayer]"]
  R13 = Resistor [tolerance=±5% resistance=10k package=THT]
  D4 = Rectifier Diode [part_number=80SQ045 package="300 mil [THT]"]
  D3 = Rectifier Diode [part_number=1N4002 package="300 mil [THT]"]
  Q3 = 2N7000
  C82 = Ceramic Capacitor [capacitance=100nF voltage=20V package="100 mil [THT, multilayer]"]
  R17 = Resistor [tolerance=±5% resistance=33k package=THT]
  R4 = Resistor [tolerance=±5% resistance=1M package=THT]
  R7 = Resistor [tolerance=±5% resistance=10k package=THT]
  R3 = Resistor [tolerance=±5% resistance=2k package=THT]
  R6 = Resistor [tolerance=±5% resistance=560 package=THT]
  R5 = Resistor [tolerance=±5% resistance=10k package=THT]
  D1 = Schottky Diode [part_number=1N914 package="300 mil [THT]"]
  J2 = Screw terminal - 2 pins [package=THT]
  J1 = Screw terminal - 2 pins [package=THT]
  R1 = Resistor [tolerance=±5% resistance=100k package=THT]
  C4 = Electrolytic Capacitor [capacitance=22µF voltage=20V package="100 mil [THT, electrolytic]"]
  R2 = POT [package=3362u]
  C2 = Electrolytic Capacitor [capacitance=47µF voltage=20V package="100 mil [THT, electrolytic]"]
  C6 = Electrolytic Capacitor [capacitance=22µF voltage=20V package="100 mil [THT, electrolytic]"]
  C8 = Ceramic Capacitor [capacitance=100nF package="100 mil [THT, multilayer]"]
  C1 = Ceramic Capacitor [capacitance=100nF package="100 mil [THT, multilayer]"]
  R12 = Resistor [tolerance=±5% resistance=27k package=THT]
  D2 = Zener Diode [part_number=1N4747 breakdown_voltage=20V package="300 mil [THT]"]
  LED2 = LEDs [package=led10mm]
  R57 = Resistor [tolerance=±5% resistance=2k package=THT]
  R14 = Resistor [tolerance=±5% resistance=68 package=THT]
  LED3 = LEDs [package=led10mm]
  R10 = Resistor [tolerance=±5% resistance=2k package=THT]
  Q5 = 2N7000
  D5 = TL431 [part_number=TL431]
  R51 = Resistor [tolerance=±5% resistance=10k package=THT]
  R52 = Resistor [tolerance=±5% resistance=10k package=THT]
  IC2 = Voltage Regulator [package=to-92]
  Q1 = 2N7000
  R53 = Resistor [tolerance=±5% resistance=150k package=THT]
  R54 = Resistor [tolerance=±5% resistance=68k package=THT]
  R55 = Resistor [tolerance=±5% resistance=150k package=THT]
  R56 = Resistor [tolerance=±5% resistance=68k package=THT]
  C9 = Ceramic Capacitor [capacitance=100nF package="100 mil [THT, multilayer]"]
  Part1 = Arduino Prototyping Shield
  R58 = Resistor [tolerance=±5% resistance=4M package=THT]
  R59 = Resistor [tolerance=±5% resistance=4M package=THT]
  R60 = Resistor [tolerance=±5% resistance=100k package=THT]
  R61 = Resistor [tolerance=±5% resistance=100k package=THT]
  R62 = Resistor [tolerance=±5% resistance=68k package=THT]
  R63 = Resistor [tolerance=±5% resistance=150k package=THT]
  Q4 = Basic FET P-Channel [part_number=IRF4905 package="TO220 [THT]"]
  Pad1 = Pad [width=8.35584800345582 height=11.9832103906693 connect=center]
  Pad2 = Pad [width=7.90222222222222 height=9.03111111111111 connect=center]
  Pad3 = Pad [width=3.59165886377262 height=12.3836006284467 connect=center]

nets:
  GND: C83.0, U2.Ground, U1.connector3, C3.1, Q3.connector0, C82.0, R3.Pin_1, D1.anode, J2.pin2, J1.pin2, C4.-, C2.-, C6.-, C8.1, C1.0, Q5.connector0, D5.connector1, R52.Pin_1, IC2.IN, Q1.connector0, R54.Pin_0, R56.Pin_0, Part1.GND, R59.Pin_1, R60.Pin_1, R62.Pin_1
  V+: C83.1, R15.Pin_0, U2.Reset, U2.Vcc_Supply_Voltage, U1.connector7, C82.1, R17.Pin_1, R6.Pin_1, C6.+, R57.Pin_1, IC2.GND
  555_treshold: R15.Pin_1, R50.Pin_0, U2.Threshold, C2.+, R58.Pin_1
  N1: R50.Pin_1, U2.Discharge
  gate1: U2.Trigger, U1.connector0, Q3.connector2, R17.Pin_0, R4.Pin_1, Q5.connector1, Q1.connector1
  N2: U2.Output, Q3.connector1, R61.Pin_0
  N3: U2.Control_Voltage, C3.0
  input-: U1.connector1, R5.Pin_1, D1.cathode, C1.1
  N4: U1.connector2, R4.Pin_0, R7.Pin_1
  VBattDiv: U1.connector4, R53.Pin_1, R54.Pin_1, Part1.A0
  PV+Div: U1.connector5, R55.Pin_1, R56.Pin_1, Part1.A1
  N5: U1.connector6, LED2.C
  N6: R13.Pin_0, Q4.gate
  N7: R13.Pin_1, R12.Pin_0, D2.anode, R14.Pin_0, C9.1
  VBatt: D4.cathode, J2.pin1, R1.Pin_1, R53.Pin_0, Pad2.pad
  N8: D4.anode, Q4.drain, Pad1.pad
  Vreg_in: D3.cathode, C8.0, R10.Pin_0, IC2.OUT
  PV+: D3.anode, J1.pin1, R12.Pin_1, D2.cathode, R55.Pin_0, C9.0, Q4.source, Pad3.pad
  N9: R7.Pin_0, R6.Pin_0, C4.+, D5.connector2, R51.Pin_1
  N10: R3.Pin_0, R2.E
  N11: R5.Pin_0, R2.S
  N12: R1.Pin_0, R2.A
  N13: LED2.A, R57.Pin_0
  N14: R14.Pin_1, Q1.connector2
  N15: LED3.A, R10.Pin_1
  Led3: LED3.C, Q5.connector2, R63.Pin_0
  N16: D5.connector0, R51.Pin_0, R52.Pin_0
  N17: Part1.A2, R58.Pin_0, R59.Pin_0
  N18: Part1.A3, R60.Pin_0, R61.Pin_1
  N19: Part1.A5, R62.Pin_0, R63.Pin_1

notes:
  LM385 part is used as a pin compatible comparator LM193, LM2903, LM293, LM393.
  The Voltage regulator is used instead of an LM78L08 and are NOT pin compatible.
  Stripboard fr Kjell & Co har 38 banor & ca 62 hål per bana.
