# Fritzing sketch id2633_Modo_Semaforo_Nicovenko_0 (saved by Fritzing 0.9.3b)
breadboards: 1

parts:
  Componente1 = Arduino Uno (Rev3)
  R1 = Resistor [tolerance=±5% resistance=220 package=THT]
  R2 = Resistor [tolerance=±5% resistance=220 package=THT]
  R3 = Resistor [tolerance=±5% resistance=220 package=THT]
  LED1 = LED - 5mm [color="Green (560nm)" package="5 mm [THT]"]
  LED2 = LED - 5mm [color="Red (633nm)" package="5 mm [THT]"]
  LED3 = LED - 5mm [color="White (8000K)" package="5 mm [THT]"]
  R4 = Rotary Potentiometer (Small) [maximum_resistance=100kΩ package=THT]
  S1 = Pushbutton [package="[THT]"]

nets:
  N1: Componente1.D2, LED2.anode
  N2: Componente1.D3_PWM, LED3.anode
  N3: Componente1.D4, LED1.anode
  N4: Componente1.D5_PWM, R4.leg2, S1.Pin_3, S1.Pin_4
  N5: Componente1.5V, S1.Pin_1, S1.Pin_2
  N6: Componente1.GND, R1.Pin_1, R2.Pin_1, R3.Pin_1, R4.leg1
  N7: R1.Pin_0, LED3.cathode
  N8: R2.Pin_0, LED1.cathode
  N9: R3.Pin_0, LED2.cathode

notes:
  MODO SEMAFORO NICOVENKO
