# Fritzing sketch id2634_Knock_0 (saved by Fritzing 0.8.6b)
circuit board: 6.88566cm x 5.36311cm
breadboards: 2

parts:
  J2 = Piezo Speaker
  R5 = Resistor [resistance=1M tolerance=±5% package=THT]
  Arduino1 = Arduino Uno (Rev3)
  part = Resistor [tolerance=±5% resistance=220 package=THT]  # not connected

nets:
  N1: J2.pin1, R5.Pin_0, Arduino1.GND
  N2: J2.pin2, R5.Pin_1, Arduino1.A0

notes:
  A Piezo is an electronic device that can both be used to play tones and to detect tones. In this project, a Piezo captures a knock and sends a string "Knock!" back to the computer over the serial port. In order to see this text you can use the Arduino serial monitor.
  http://arduino.cc/en/Tutorial/Knock
