# Fritzing sketch id2635_eqs_0 (saved by Fritzing 0.8.7b)
circuit board: 3.25977cm x 3.21755cm
breadboards: 1

parts:
  R3 = Resistor [tolerance=±5% resistance=47k package=THT]
  R4 = Resistor [tolerance=±5% resistance=47k package=THT]
  R5 = Resistor [tolerance=±5% resistance=6.8k package=THT]
  R = Resistor [tolerance=±5% resistance=0 package=THT]
  R_2 = Resistor [tolerance=±5% resistance=0 package=THT]
  C2 = Ceramic Capacitor [capacitance=100nF package="200 mil [THT, multilayer]"]
  C1 = Ceramic Capacitor [capacitance=100nF package="200 mil [THT, multilayer]"]
  Power = screw terminal, 3 pins
  output = Screw terminal - 2 pins [package=THT]
  input = Screw terminal - 2 pins [package=THT]
  R1 = Resistor [tolerance=±5% resistance=10k package=THT]
  C3 = Electrolytic Capacitor [capacitance=10µF package="100 mil [THT, electrolytic]"]
  C4 = Electrolytic Capacitor [capacitance=10µF package="100 mil [THT, electrolytic]"]
  R2 = Resistor [tolerance=±5% resistance=10k package=THT]
  Gain = Rotary Potentiometer (Large) [maximum_resistance=100kΩ package=THT]
  TL072 = Dual Op-Amp [package=dip08]

nets:
  N1: R3.Pin_0, R4.Pin_1, Gain.leg2, TL072.A_-IN
  N2: R3.Pin_1, C4.+, Gain.leg1, TL072.A_OUT
  N3: R4.Pin_0, C3.+
  N4: R5.Pin_0, Gain.wiper
  N5: R5.Pin_1, TL072.B_+IN
  N6: R.Pin_0, C1.1
  N7: R.Pin_1, TL072.B_-IN, TL072.B_OUT
  N8: R_2.Pin_0, C2.1, C1.0, TL072.A_+IN
  GND: R_2.Pin_1, C2.0, Power.pin1, output.pin2, input.pin1, R1.Pin_0, R2.Pin_1
  -12V: Power.pin2, TL072.A_V-
  12V: Power.pin3, TL072.A_V+
  N9: output.pin1, C4.-, R2.Pin_0
  N10: input.pin2, R1.Pin_1, C3.-

notes:
  Gnd
  V-
  V+
  + Input -
  - Output +
  Little, Creepy, One band Eq by Nathan.C
  2014
