# Fritzing sketch id2636_modulo_rfcr522_concuatro_reles_y_un_servo_0 (saved by Fritzing 0.9.0b)
breadboards: 1

parts:
  Parte1 = rc522
  Parte2 = Arduino Uno (Rev3)
  J1 = Basic Servo
  LED1 = LED - 5mm [color="Red (633nm)" package="5 mm [THT]"]
  LED2 = LED - 5mm [color="Red (633nm)" package="5 mm [THT]"]
  LED3 = smd LED [color="Red (633nm)" package="0805 [SMD]"]
  LED4 = smd LED [color="Red (633nm)" package="0805 [SMD]"]
  LED5 = smd LED [color="Red (633nm)" package="0805 [SMD]"]
  LED6 = smd LED [color="Red (633nm)" package="0805 [SMD]"]
  R1 = Resistor [tolerance=±5% resistance=220 package=THT]
  R2 = Resistor [tolerance=±5% resistance=220 package=THT]
  R3 = Resistor [tolerance=±5% resistance=220 package=THT]
  R4 = Resistor [tolerance=±5% resistance=220 package=THT]
  R5 = Resistor [tolerance=±5% resistance=220 package=THT]
  R6 = Resistor [tolerance=±5% resistance=220 package=THT]

nets:
  N1: Parte1.connector8, Parte2.D10_PWM/SS
  N2: Parte1.connector9, Parte2.D13/SCK
  N3: Parte1.connector10, Parte2.D11_PWM/MOSI
  N4: Parte1.connector11, Parte2.D12/MISO
  GND: Parte1.connector13, Parte2.GND, J1.gnd, R1.Pin_1, R2.Pin_1, R3.Pin_1, R4.Pin_1, R5.Pin_1, R6.Pin_1
  N5: Parte1.connector14, Parte2.D5_PWM
  N6: Parte1.connector15, Parte2.3V3
  N7: Parte2.D3_PWM, LED2.anode
  N8: Parte2.D6_PWM, LED1.anode
  N9: Parte2.D7, J1.pulse
  VIN: Parte2.VIN, J1.vcc
  N10: LED1.cathode, R1.Pin_0
  N11: LED3.cathode, R3.Pin_0
  N12: LED4.cathode, R4.Pin_0
  N13: LED5.cathode, R5.Pin_0
  N14: LED6.cathode, R6.Pin_0

notes:
  modulo de cuatro reles de 5v comprado en alliexpres
