# Fritzing sketch id2637_modulo_rele2_0 (saved by Fritzing 0.9.2b)
circuit board: 6.07503cm x 1.72778cm
breadboards: 1

parts:
  Q1 = TRANSISTOR_NPN [part_number=BC548 package=to-92-ammo]
  R1 = Resistor [tolerance=±5% resistance=1k package="0805 [SMD]"]
  OPTOACOPLADOR_4N25 = Optocoupler 4N25
  R2 = Resistor [tolerance=±5% resistance=1k package="0805 [SMD]"]
  D1 = Diode [package=diode-1n4148]
  RELÊ_12V = RELAY [package=relay-g5q]
  5V = Screw terminal - 2 pins [package=THT]
  12V = Screw terminal - 2 pins [package=THT]
  J3 = screw terminal, 3 pins

nets:
  N1: Q1.E, 12V.pin2
  N2: Q1.B, R2.Pin_1
  N3: Q1.C, D1.A, RELÊ_12V.COIL2
  N4: R1.Pin_0, 5V.pin1
  N5: R1.Pin_1, OPTOACOPLADOR_4N25.connector0
  N6: OPTOACOPLADOR_4N25.connector1, 5V.pin2
  N7: OPTOACOPLADOR_4N25.connector3, R2.Pin_0
  N8: OPTOACOPLADOR_4N25.connector4, D1.C, RELÊ_12V.COIL1, 12V.pin1
  N9: RELÊ_12V.MAIN, RELÊ_12V.NO, RELÊ_12V.NC, J3.pin1, J3.pin2, J3.pin3

notes:
  5V
