# Fritzing sketch id2638_garagedeur_klok_lcd_v11_0 (saved by Fritzing 0.9.3b)
breadboards: 1

parts:
  Onderdeel1 = Arduino Uno (Rev3)  # not connected
  Onderdeel2 = Arduino GSM Shield
  R1 = Resistor [tolerance=±5% resistance=10k package=THT]
  R2 = Resistor [tolerance=±5% resistance=10k package=THT]
  R3 = Resistor [tolerance=±5% resistance=10k package=THT]
  R4 = Resistor [tolerance=±5% resistance=10k package=THT]
  Tiny_RTC1 = tinyRTC
  S5 = Reed switch [package=THT]
  S6 = Reed switch [package=THT]
  S7 = Reed switch [package=THT]
  S8 = Reed switch [package=THT]
  U1 = 2ChannelRelay
  LCM1602_IIC1 = generic_ic_dip_22_300mil.fzp [part_number="LCM1602 IIC" chip_label="LCM1602 IIC"]
  4x20_LCD_screen_w/Blue_Screen1 = 4x20 LCD Blue Screen
  Onderdeel3 = Arduino Prototyping Shield
  J1 = female pin header, 4 pins [form="♀ (female)"]
  J2 = female pin header, 4 pins [form="♀ (female)"]
  J3 = female pin header, 4 pins [form="♀ (female)"]
  J4 = female pin header, 4 pins [form="♀ (female)"]
  J5 = female pin header, 4 pins [form="♀ (female)"]
  J6 = female pin header, 4 pins [form="♀ (female)"]
  R5 = Resistor [tolerance=±5% resistance=10k package=THT]
  R6 = Resistor [tolerance=±5% resistance=10k package=THT]
  R7 = Resistor [tolerance=±5% resistance=10k package=THT]
  R8 = Resistor [tolerance=±5% resistance=10k package=THT]
  J7 = female pin header, 4 pins [form="♀ (female)"]

nets:
  N1: Onderdeel2.A5/SCL, Tiny_RTC1.connector1, LCM1602_IIC1.connector19
  N2: Onderdeel2.A4/SDA, Tiny_RTC1.connector2, LCM1602_IIC1.connector18
  N3: Onderdeel2.PWM_D9, U1.connector2
  N4: Onderdeel2.D8, U1.connector3
  N5: Onderdeel2.5V, Tiny_RTC1.connector3, S5.pin_2, S6.pin_2, S7.pin_2, S8.pin_2, U1.connector0, LCM1602_IIC1.connector17
  N6: Onderdeel2.AGND, R1.Pin_1, R2.Pin_1, R3.Pin_1, R4.Pin_1, Tiny_RTC1.connector4, U1.connector1, LCM1602_IIC1.connector16
  N7: Onderdeel2.A0, R1.Pin_0, S5.pin_1
  N8: Onderdeel2.A1, R2.Pin_0, S6.pin_1
  N9: Onderdeel2.A2, R3.Pin_0, S7.pin_1
  N10: Onderdeel2.A3, R4.Pin_0, S8.pin_1
  N11: LCM1602_IIC1.connector0, 4x20_LCD_screen_w/Blue_Screen1.connector0
  N12: LCM1602_IIC1.connector1, 4x20_LCD_screen_w/Blue_Screen1.connector1
  N13: LCM1602_IIC1.connector2, 4x20_LCD_screen_w/Blue_Screen1.connector2
  N14: LCM1602_IIC1.connector3, 4x20_LCD_screen_w/Blue_Screen1.connector3
  N15: LCM1602_IIC1.connector4, 4x20_LCD_screen_w/Blue_Screen1.connector4
  N16: LCM1602_IIC1.connector5, 4x20_LCD_screen_w/Blue_Screen1.connector5
  N17: LCM1602_IIC1.connector6, 4x20_LCD_screen_w/Blue_Screen1.connector6
  N18: LCM1602_IIC1.connector7, 4x20_LCD_screen_w/Blue_Screen1.connector7
  N19: LCM1602_IIC1.connector8, 4x20_LCD_screen_w/Blue_Screen1.connector8
  N20: LCM1602_IIC1.connector9, 4x20_LCD_screen_w/Blue_Screen1.connector9
  N21: LCM1602_IIC1.connector10, 4x20_LCD_screen_w/Blue_Screen1.connector10
  N22: LCM1602_IIC1.connector11, 4x20_LCD_screen_w/Blue_Screen1.connector11
  N23: LCM1602_IIC1.connector12, 4x20_LCD_screen_w/Blue_Screen1.connector12
  N24: LCM1602_IIC1.connector13, 4x20_LCD_screen_w/Blue_Screen1.connector13
  N25: LCM1602_IIC1.connector14, 4x20_LCD_screen_w/Blue_Screen1.connector14
  N26: LCM1602_IIC1.connector15, 4x20_LCD_screen_w/Blue_Screen1.connector15
  N27: Onderdeel3.D12, J5.pin4
  N28: Onderdeel3.+5V, Onderdeel3.N$39, Onderdeel3.N$54, Onderdeel3.N$55, Onderdeel3.N$72, Onderdeel3.N$73, Onderdeel3.N$75, Onderdeel3.N$81, Onderdeel3.N$87, Onderdeel3.N$238, Onderdeel3.N$239, Onderdeel3.N$276, Onderdeel3.N$292, Onderdeel3.N$327, Onderdeel3.N$402, J1.pin3, J2.pin3, J3.pin4, J6.pin2, J6.pin4, J7.pin2, J7.pin4
  N29: Onderdeel3.D8, Onderdeel3.N$85, Onderdeel3.N$86, J3.pin3
  N30: Onderdeel3.D9, Onderdeel3.N$77, J3.pin2
  N31: Onderdeel3.SCL, Onderdeel3.N$78, Onderdeel3.N$79, Onderdeel3.N$178, Onderdeel3.N$190, J1.pin1, J2.pin1
  N32: Onderdeel3.SDA, Onderdeel3.N$65, Onderdeel3.N$66, Onderdeel3.N$67, Onderdeel3.N$74, J1.pin2, J2.pin2
  N33: Onderdeel3.A0, Onderdeel3.N$405
  N34: Onderdeel3.A1, Onderdeel3.N$398
  N35: Onderdeel3.A2, Onderdeel3.N$93
  N36: Onderdeel3.A3, Onderdeel3.N$368
  N37: Onderdeel3.GND, Onderdeel3.N$41, Onderdeel3.N$42, Onderdeel3.N$69, Onderdeel3.N$76, Onderdeel3.N$84, Onderdeel3.N$90, Onderdeel3.N$177, Onderdeel3.N$295, Onderdeel3.N$311, J1.pin4, J2.pin4, J3.pin1, R5.Pin_1, R6.Pin_1, R7.Pin_1, R8.Pin_1
  N38: Onderdeel3.N$321, J4.pin1
  N39: Onderdeel3.N$322, J4.pin2
  N40: Onderdeel3.N$324, J4.pin3
  N41: Onderdeel3.N$325, J4.pin4
  N42: Onderdeel3.N$369, Onderdeel3.N$371, R8.Pin_0, J7.pin3
  N43: Onderdeel3.N$380, Onderdeel3.N$381, R7.Pin_0, J7.pin1
  N44: Onderdeel3.N$397, J5.pin3
  N45: Onderdeel3.N$399, Onderdeel3.N$400, J6.pin3, R6.Pin_0
  N46: Onderdeel3.N$401, J5.pin2
  N47: Onderdeel3.N$404, J5.pin1
  N48: Onderdeel3.N$406, Onderdeel3.N$409, J6.pin1, R5.Pin_0
