# Fritzing sketch id2639_444_all_in_one2_0 (saved by Fritzing 0.7.12b)

parts:
  R1 = Resistor [tolerance=±5% resistance=220 package=THT]
  R2 = Resistor [tolerance=±5% resistance=220 package=THT]
  R3 = Resistor [tolerance=±5% resistance=220 package=THT]
  R4 = Resistor [tolerance=±5% resistance=220 package=THT]
  R5 = Resistor [tolerance=±5% resistance=220 package=THT]
  R6 = Resistor [tolerance=±5% resistance=220 package=THT]
  R7 = Resistor [tolerance=±5% resistance=220 package=THT]
  R8 = Resistor [tolerance=±5% resistance=220 package=THT]
  R9 = Resistor [tolerance=±5% resistance=220 package=THT]
  R10 = Resistor [tolerance=±5% resistance=220 package=THT]
  R11 = Resistor [tolerance=±5% resistance=220 package=THT]
  R12 = Resistor [tolerance=±5% resistance=220 package=THT]
  Q1 = NPN-Transistor [package="TO92 [THT]"]
  R13 = Resistor [tolerance=±5% resistance=22k package=THT]
  R14 = Resistor [tolerance=±5% resistance=22k package=THT]
  R15 = Resistor [tolerance=±5% resistance=22k package=THT]
  R16 = Resistor [tolerance=±5% resistance=22k package=THT]
  Q2 = NPN-Transistor [package="TO92 [THT]"]
  Q4 = NPN-Transistor [package="TO92 [THT]"]
  R17 = Resistor [tolerance=±5% resistance=220 package=THT]
  R18 = Resistor [tolerance=±5% resistance=220 package=THT]
  R19 = Resistor [tolerance=±5% resistance=220 package=THT]
  R20 = Resistor [tolerance=±5% resistance=220 package=THT]
  J1 = male pin header, 6 pins [form="♂ (male)"]
  J3 = male pin header, 7 pins [form="♂ (male)"]
  J2 = male pin header, 8 pins [form="♂ (male)"]
  Q3 = NPN-Transistor [package="TO92 [THT]"]

nets:
  N1: R1.Pin_1, J3.pin2
  N2: R2.Pin_1, J3.pin3
  N3: R3.Pin_1, J3.pin4
  N4: R4.Pin_1, J3.pin5
  N5: R5.Pin_1, J1.pin2
  N6: R6.Pin_1, J2.pin7
  N7: R7.Pin_1, J1.pin1
  N8: R8.Pin_1, J2.pin8
  N9: R9.Pin_1, J3.pin6
  N10: R10.Pin_1, J3.pin7
  N11: R11.Pin_1, J2.pin4
  N12: R12.Pin_0, J2.pin3
  N13: Q1.B, R14.Pin_0
  N14: Q1.C, Q2.C, Q4.C, J3.pin1, Q3.C
  N15: R13.Pin_0, Q2.B
  N16: R13.Pin_1, J1.pin3
  N17: R14.Pin_1, J1.pin4
  N18: R15.Pin_0, Q3.B
  N19: R15.Pin_1, J1.pin5
  N20: R16.Pin_0, Q4.B
  N21: R16.Pin_1, J1.pin6
  N22: R17.Pin_1, J2.pin1
  N23: R18.Pin_1, J2.pin2
  N24: R19.Pin_1, J2.pin6
  N25: R20.Pin_1, J2.pin5

notes:
  L4
  C4
  C8
  C16
  L1
  L2
  L3
  C12
  C9
  C13
  C3
  C2
  C6
  C7
  C10
  C11
  C14
  C15
  C1
  C5
  3
  2013
  MONOCHROME LED CUBE
  4
