# Fritzing sketch id2640_Arduino_LCD_lesson_0 (saved by Fritzing 0.9.3b)
breadboards: 1

parts:
  Part1 = Arduino Uno (Rev3)
  hc-sr1 = hc-sr04
  LCD1 = LCD screen  # not connected

nets:
  N1: Part1.D12/MISO, hc-sr1.Echo
  N2: Part1.D13/SCK, hc-sr1.Trig
  5V: Part1.5V, hc-sr1.VCC
  GND: Part1.GND, hc-sr1.GND
