# Fritzing sketch id2641_us_servo_0 (saved by Fritzing 0.9.3b)
breadboards: 1

parts:
  hc-sr1 = hc-sr04
  Composant1 = Arduino Uno (Rev3)
  J1 = Basic Servo

nets:
  VCC: hc-sr1.VCC, Composant1.5V
  N1: hc-sr1.Trig, Composant1.D9_PWM
  N2: hc-sr1.Echo, Composant1.D10_PWM/SS
  GND: hc-sr1.GND, Composant1.GND, J1.gnd
  N3: Composant1.D11_PWM/MOSI, J1.pulse
