# Fritzing sketch id2642_dht22_0 (saved by Fritzing 0.9.3b)
breadboards: 1

parts:
  Composant1 = Arduino Uno (Rev3)
  DHT1 = DHT22_Humidity_and_Temperature_Sensor
  R1 = Resistor [tolerance=±5% resistance=10k package="2512 [SMD]"]

nets:
  N1: Composant1.D2, DHT1.connector2, R1.Pin_1
  N2: Composant1.5V, DHT1.connector1, R1.Pin_0
  N3: Composant1.GND, DHT1.connector4
