# Fritzing sketch id2643_capteur_IR_0 (saved by Fritzing 0.9.3b)
breadboards: 1

parts:
  Composant1 = PIR D-SUN HC-SR501
  Composant2 = Arduino Uno (Rev3)

nets:
  N1: Composant1.connector0, Composant2.5V
  N2: Composant1.connector1, Composant2.D2
  N3: Composant1.connector2, Composant2.GND
