# Fritzing sketch id2644_ConexionATmega328_0 (saved by Fritzing 0.9.2b)
breadboards: 1

parts:
  C1 = Electrolytic Capacitor [capacitance=10µF package="100 mil [THT, electrolytic]"]
  Power_plug1 = Power plug
  U1 = Voltage Regulator - 5V [package="TO220 [THT]"]
  C2 = Electrolytic Capacitor [capacitance=10µF package="100 mil [THT, electrolytic]"]
  LED1 = LED - 5mm [color="Red (633nm)" package="5 mm [THT]"]
  R1 = Resistor [tolerance=±5% resistance=220 package=THT]
  S1 = Pushbutton [package="[THT]"]
  XTAL1 = Crystal [frequency="16 Mhz" package=THT]
  R2 = Resistor [tolerance=±5% resistance=10k package=THT]
  C3 = Ceramic Capacitor [capacitance=22pF package="100 mil [THT, multilayer]"]
  C4 = Ceramic Capacitor [capacitance=22pF package="100 mil [THT, multilayer]"]
  LED2 = LED - 5mm [color="Green (555nm)" package="5 mm [THT]"]
  R3 = Resistor [tolerance=±5% resistance=220 package=THT]
  U2 = atmega328 [package=dip]
  FTDI = FTDI Basic Programmer

nets:
  GND: C1.-, C3.1, C4.1, R3.Pin_1, U2.GND, FTDI.GND
  N1: C1.+, U1.output_voltage, LED1.anode, S1.Pin_3, S1.Pin_4, R2.Pin_0, U2.VCC, U2.AVCC, U2.AREF, FTDI.POWER
  GND_2: Power_plug1.GND, U1.GND, C2.-, R1.Pin_1
  N2: Power_plug1.VCC, U1.input_voltage, C2.+
  N3: LED1.cathode, R1.Pin_0
  N4: S1.Pin_1, S1.Pin_2, R2.Pin_1, U2.RESET
  N5: XTAL1.pin_0, C3.0, U2.XLAT1
  N6: XTAL1.pin_1, C4.0, U2.XLAT2
  N7: LED2.cathode, R3.Pin_0
  N8: LED2.anode, U2.D13
  N9: U2.D0_(RX), FTDI.TXO
  N10: U2.D1_(TX), FTDI.RXI
