# Fritzing sketch id2645_Montaxe_1_0 (saved by Fritzing 0.9.3b)
circuit board: 8.46667cm x 5.64444cm
breadboards: 1

parts:
  R1 = Resistor [tolerance=±5% resistance=220 package=THT]  # not connected
  LED1 = LED - 5mm [color="Red (633nm)" package="5 mm [THT]"]
  S1 = Pushbutton [package="[THT]"]
  Componente1 = Arduino Uno (Rev3)

nets:
  N1: LED1.cathode, Componente1.GND
  N2: LED1.anode, S1.Pin_1, S1.Pin_2
  N3: S1.Pin_3, S1.Pin_4
