# Fritzing sketch id2646_Mood_coaster2_0 (saved by Fritzing 0.9.1b)
breadboards: 1

parts:
  Part1 = Arduino Pro Mini v13
  Part2 = FTDI Basic Programmer
  neopixel1 = Neopixel_24_Ring
  S1 = Pushbutton [package="[THT]"]
  R2 = Resistor [tolerance=±5% resistance=220 package=THT]
  R3 = Temperature Sensor (Thermistor) [thermistor_type=NTC package=THT]

nets:
  N1: Part1.DTR, Part2.DTR
  N2: Part1.D0/TX, Part2.RXI
  N3: Part1.D1/RX, Part2.TXO
  N4: Part1.VCC, Part2.POWER, neopixel1.connector2
  GND: Part1.GND, Part2.CTS, Part2.GND, neopixel1.connector1, R2.Pin_0
  N5: Part1.A0, R2.Pin_1, R3.pin_0
  N6: Part1.D6_PWM, R3.pin_1
  N7: Part1.D5_PWM, neopixel1.connector3
  N8: Part1.D4, S1.Pin_3, S1.Pin_4
  N9: Part1.D3_PWM, S1.Pin_1, S1.Pin_2
