# Fritzing sketch id264_agirs_dht_os21_0 (saved by Fritzing 0.9.3b)
circuit board: 2.87389cm x 6.08467cm

parts:
  ESP8266 = ESP8266_module [part_number=ESP8266]
  Nano_R3 = Arduino Nano (Rev3.0)
  R2 = Resistor [tolerance=±5% resistance=1k package=THT]
  R1 = Resistor [tolerance=±5% resistance=10k package=THT]
  R3 = Resistor [tolerance=±5% resistance=2.2k package=THT]
  IR_LED1 = LED - 5mm [color="Infrared (940nm)" package="5 mm [THT]"]
  Q3 = NPN-Transistor [package="TO92 [THT]"]
  Q4 = NPN-Transistor [package="TO92 [THT]"]
  TX434 = female pin header, 3 pins [form="♀ (female)"]
  DHT12 = Humidity and Temperature Sensor RHT03
  5V1 = Screw terminal - 2 pins [package=THT]
  R5 = Resistor [tolerance=±5% resistance=68 package=THT]
  R6 = Resistor [tolerance=±5% resistance=68 package=THT]
  R7 = Resistor [tolerance=±5% resistance=68 package=THT]
  RGBLED = RGB LED (com. cathode, rbg) [package="5 mm [THT]"]
  R8 = Resistor [tolerance=±5% resistance=68 package=THT]
  R4 = Resistor [tolerance=±5% resistance=220 package=THT]

nets:
  N1: ESP8266.connector0, R2.Pin_0, R3.Pin_0
  N2: ESP8266.connector1, Nano_R3.3V3, R1.Pin_1
  N3: ESP8266.connector5, R1.Pin_0
  N4: ESP8266.connector6, Nano_R3.GND, R3.Pin_1
  N5: ESP8266.connector7, Nano_R3.D2
  N6: Nano_R3.D3, R2.Pin_1
  N7: Nano_R3.D4, DHT12.Data-signal, R4.Pin_1
  N8: Nano_R3.D5, Q4.C
  N9: Nano_R3.D6, R8.Pin_0
  N10: Nano_R3.D7, TX434.pin1
  N11: Nano_R3.D8, Q3.C
  VIN: Nano_R3.VIN, Nano_R3.5V, Q3.E, Q4.E, TX434.pin2, DHT12.Vcc, 5V1.pin1, R4.Pin_0
  N12: Nano_R3.A2, R7.Pin_0
  N13: Nano_R3.A1, R6.Pin_0
  N14: Nano_R3.A0, R5.Pin_0
  N15: IR_LED1.cathode, Q3.B, Q4.B, TX434.pin3, DHT12.GND_2, 5V1.pin2, RGBLED.common_cathode
  N16: IR_LED1.anode, R8.Pin_1
  N17: R5.Pin_1, RGBLED.green_anode
  N18: R6.Pin_1, RGBLED.blue_anode
  N19: R7.Pin_1, RGBLED.red_anode
