# Fritzing sketch id2650_lilypad1_0 (saved by Fritzing 0.9.0b)

parts:
  Part1 = LilyPad Coin Cell Battery Holder
  Part2 = LilyPad LED
  Part3 = LilyPad LED
  Part4 = LilyPad LED
  Part5 = LilyPad LED
  Part6 = LilyPad LED
  Part7 = LilyPad LED
  Part8 = LilyPad LED
  Part9 = LilyPad LED
  Part10 = LilyPad LED
  Part11 = LilyPad LED

nets:
  N1: Part1.-, Part2.-, Part3.-, Part5.-, Part6.-, Part7.-, Part8.-, Part9.-, Part10.-, Part11.-
  N2: Part1.+, Part2.+, Part3.+, Part4.+, Part5.+, Part6.+, Part7.+, Part8.+, Part9.+, Part10.+, Part11.+
