# Fritzing sketch id2651_morse_code_0 (saved by Fritzing 0.9.2b)
breadboards: 1

parts:
  Part1 = Arduino Uno (Rev3)
  R1 = Resistor [tolerance=±5% resistance=220 package=THT]  # not connected
  S1 = Pushbutton [package="[THT]"]  # not connected
  J1 = Piezo Speaker
  S2 = Pushbutton [package="[THT]"]
  R2 = Resistor [tolerance=±5% resistance=10k package=THT]  # not connected
  R3 = Resistor [tolerance=±5% resistance=330 package=THT]

nets:
  N1: Part1.D9_PWM, R3.Pin_0
  N2: Part1.D2, S2.Pin_3, S2.Pin_4
  N3: Part1.5V, S2.Pin_1, S2.Pin_2
  N4: Part1.GND, J1.pin1
  N5: J1.pin2, R3.Pin_1
