# Fritzing sketch id2653_FNM068RGYQFMYQD_(4)_0 (saved by Fritzing 0.9.1b)

parts:
  Arduino2 = Arduino
  LED1 = LED - 5mm [color="Red (633nm)" package="5 mm [THT]"]

nets:
  N1: Arduino2.GND, LED1.cathode
  N2: Arduino2.D13, LED1.anode
