# Fritzing sketch id2654_SCHEMATIC_0 (saved by Fritzing 0.9.0b)
breadboards: 1

parts:
  R1 = Resistor [tolerance=±5% resistance=220 package=THT]
  LED1 = LED - 5mm [color="Red (633nm)" package="5 mm [THT]"]
  Part1 = Arduino Uno (Rev3)

nets:
  N1: R1.Pin_0, LED1.cathode
  N2: R1.Pin_1, Part1.GND
  N3: LED1.anode, Part1.D6_PWM

notes:
  Components REQD.:
  Arduino UNO
  USB Printer Cable
  Solderless Breadboard
  2 Jumper Wires
  LED
  220 Ohm Resistance
