# Fritzing sketch id2655_Morse_Sketch_0 (saved by Fritzing 0.9.2b)
breadboards: 1

parts:
  Part1 = Arduino Uno (Rev3)
  LCD1 = LCD screen
  R1 = Resistor [tolerance=±5% resistance=220 package=THT]

nets:
  N1: Part1.D8, LCD1.E
  N2: Part1.D9_PWM, LCD1.DB4
  N3: Part1.D10_PWM/SS, LCD1.DB5
  N4: Part1.D11_PWM/MOSI, LCD1.DB6
  N5: Part1.D12/MISO, LCD1.DB7
  N6: Part1.D7, LCD1.RS
  N7: LCD1.VSS, LCD1.V0, LCD1.R/W, LCD1.LED-
  N8: LCD1.VDD, R1.Pin_0
  N9: LCD1.LED+, R1.Pin_1
