# Fritzing sketch id2656_Untitled_Sketch_0 (saved by Fritzing 0.8.7b)
breadboards: 1

parts:
  S1 = Pushbutton [package="[THT]"]
  LED1 = LED - 5mm [color="Red (633nm)" package="5 mm [THT]"]
  Part1 = Arduino Uno (Rev3)
  R1 = Resistor [package="2010 [SMD]"]
  LED2 = LED - 5mm [color="Green (570nm)" package="5 mm [THT]"]

nets:
  N1: S1.Pin_1, S1.Pin_2, LED1.anode, Part1.D2
  N2: S1.Pin_3, S1.Pin_4, Part1.5V
  N3: LED1.cathode, R1.Pin_0
  N4: Part1.D13/SCK, LED2.anode
  N5: Part1.GND, R1.Pin_1, LED2.cathode
