# Fritzing sketch id2657_MOSFET_Motor_0 (saved by Fritzing 0.8.7b)
circuit board: 4.99721cm x 5.36502cm
breadboards: 1

parts:
  Arduino = Arduino Uno (Rev3)
  MOSFET = Basic FET N-Channel [package="TO220 [THT]"]
  R1 = Resistor [tolerance=±5% resistance=220 package=THT]
  D2 = Rectifier Diode [part_number=1N4001 package="300 mil [THT]"]
  M3 = DC Motor

nets:
  N1: Arduino.D9_PWM, R1.Pin_1
  N2: Arduino.GND, MOSFET.source
  N3: Arduino.5V, D2.cathode, M3.pin_1
  N4: MOSFET.gate, R1.Pin_0
  N5: MOSFET.drain, D2.anode, M3.pin_2
