# Fritzing sketch id2658_Mosquito_Repellent___40khz_0 (saved by Fritzing 0.9.3b)
circuit board: 3.60763cm x 3.35997cm
breadboards: 1

parts:
  U1 = 555 Timer [package="DIP8 [THT]"]
  R2 = Resistor [tolerance=±5% resistance=1.3k package=THT]
  R3 = Resistor [tolerance=±5% resistance=1k package=THT]
  VCC1 = Battery block 9V
  C2 = Electrolytic Capacitor [capacitance=0.01µF package="100 mil [THT, electrolytic]"]
  J1 = Piezo Speaker

nets:
  N1: U1.Ground, VCC1.-, C2.+, J1.pin1
  N2: U1.Trigger, C2.-
  N3: U1.Output, J1.pin2
  N4: U1.Reset, U1.Vcc_Supply_Voltage, R3.Pin_1, VCC1.+
  N5: U1.Threshold, R2.Pin_1
  N6: U1.Discharge, R2.Pin_0, R3.Pin_0
