# Fritzing sketch id2659_detecteur_de_collision_0 (saved by Fritzing 0.9.2b)
breadboards: 1

parts:
  R1 = Resistor [tolerance=±5% resistance=10 package=THT]
  D1 = Rectifier Diode [part_number=1N4001 package="300 mil [THT]"]
  Composant1 = Arduino Uno (Rev3)
  M1 = DC Motor
  Q1 = Basic FET N-Channel [package="TO220 [THT]"]
  VCC1 = Battery block 9V
  Composant2 = SRF05 Ultrasonic Rangefinder

nets:
  N1: R1.Pin_0, Composant1.D3_PWM, Q1.gate
  N2: R1.Pin_1, Q1.source
  N3: D1.cathode, M1.pin_1, VCC1.+
  N4: D1.anode, M1.pin_2, Q1.drain
  N5: Composant1.GND, VCC1.-, Composant2.connector11
  N6: Composant1.D6_PWM, Composant2.connector10
  N7: Composant1.D7, Composant2.connector9
  N8: Composant1.VIN, Composant2.connector8
