# Fritzing sketch id265_fieldSensor_pcb_0 (saved by Fritzing 0.9.3b)
breadboards: 1

parts:
  IC1 = Voltage Regulator [package=78xxl]
  元件1 = Arduino Pro Mini (3.3V)
  J1 = Camdenboss CTB0158-4 [package=THT]
  J4 = female pin header, 3 pins [form="♀ (female)"]
  J5 = female pin header, 3 pins [form="♀ (female)"]
  R1 = Resistor [tolerance=±1% resistance=2.2k package=THT]
  R2 = Resistor [tolerance=±1% resistance=1.5k package=THT]
  R3 = Resistor [tolerance=±5% resistance=4.7k package=THT]
  R4 = Resistor [tolerance=±5% resistance=4.7k package=THT]
  J2 = JST-VHR-3N [package=THT]
  J3 = JST-VHR-3N [package=THT]

nets:
  GND: IC1.GND, 元件1.GND, J1.terminal_2, J1.terminal_3, J4.pin3, J5.pin3, R2.Pin_0, J2.pin3, J2.pin_6, J3.pin3
  N1: IC1.IN, J1.terminal_1, R1.Pin_1
  N2: IC1.OUT, 元件1.RAW
  3.3V: 元件1.VCC, J4.pin2, J5.pin2, R3.Pin_0, R4.Pin_0, J2.pin1, J2.pin_4, J3.pin1
  N3: 元件1.A7, R1.Pin_0, R2.Pin_1
  N4: 元件1.A1, J5.pin1
  N5: 元件1.A0, J4.pin1
  N6: 元件1.D9, J1.terminal_4
  N7: 元件1.D3, R4.Pin_1, J3.pin2
  N8: 元件1.D2, R3.Pin_1, J2.pin2, J2.pin_5

notes:
  溫度感測器
  濕度感測器
