# Fritzing sketch id2660_Moteur_LDR2_0 (saved by Fritzing 0.9.2b)
breadboards: 1

parts:
  Composant1 = Arduino Uno (Rev3)
  R1 = Resistor [tolerance=±5% resistance=2.2 package=THT]
  VCC1 = Battery
  R3 = Resistor [tolerance=±5% resistance=10k package=THT]
  R4 = Photocell (LDR) [package=THT]
  M1 = DC Motor
  Q1 = NPN-Transistor [package="TO92 [THT]"]

nets (from the breadboard view):
  N1: Composant1.A0, R3.Pin_1, R4.pin_0
  N2: Composant1.D13/SCK, R1.Pin_1
  N3: Composant1.5V, R4.pin_1
  N4: Composant1.GND, R3.Pin_0, Q1.E
  N5: R1.Pin_0, Q1.B
  N6: VCC1.+, M1.pin_1
