# Fritzing sketch id2661_Moteur_potard_0 (saved by Fritzing 0.9.2b)
circuit board: 8.46667cm x 5.64444cm
breadboards: 1

parts:
  R2 = Resistor [tolerance=±5% resistance=330 package=THT]
  M1 = DC Motor
  D2 = Rectifier Diode [part_number=1N4001 package="300 mil [THT]"]
  Composant1 = Arduino Uno (Rev3)
  R1 = Trimmer Potentiometer [maximum_resistance=10kΩ package=THT]
  Q1 = NPN-Transistor [part_number=N2222 package="TO92 [THT]"]

nets:
  N1: R2.Pin_0, Composant1.D3_PWM
  N2: R2.Pin_1, Q1.B
  N3: M1.pin_1, D2.anode, Q1.C
  N4: M1.pin_2, D2.cathode, Composant1.5V, R1.leg1
  N5: Composant1.A0, R1.wiper
  N6: Composant1.GND, R1.leg2, Q1.E
