# Fritzing sketch id2662_schema_prototipo_0 (saved by Fritzing 0.9.3b)

parts:
  Componente1 = Arduino Uno (Rev3)
  hc-sr1 = hc-sr04
  DFRobot_DFPlayer_Mini1 = DFRobot DFPlayer Mini [part_number=DFR0299]
  SP1 = SPEAKER [package=pcb_mount_speaker]

nets:
  N1: Componente1.D9_PWM, hc-sr1.Trig
  N2: Componente1.D10_PWM/SS, hc-sr1.Echo
  N3: Componente1.D12/MISO, DFRobot_DFPlayer_Mini1.TX
  N4: Componente1.D13/SCK, DFRobot_DFPlayer_Mini1.RX
  3V3: Componente1.3V3, DFRobot_DFPlayer_Mini1.VCC
  5V: Componente1.5V, hc-sr1.VCC
  GND: Componente1.GND, hc-sr1.GND, DFRobot_DFPlayer_Mini1.GND-1
  N5: DFRobot_DFPlayer_Mini1.SPK_1, SP1.-
  N6: DFRobot_DFPlayer_Mini1.SPK_2, SP1.+
