# Fritzing sketch id2664_OAP_Camera_Mega_0 (saved by Fritzing 0.7.11b)
breadboards: 1

parts:
  U1 = Arduino Mega
  Arduino_Ethernet_Shield1 = Arduino Ethernet Shield
  Motion_Detect = mystery part, 8 pins [chip_label=zMotion]
  Camera = mystery part, 4 pins [chip_label=Camera]

nets:
  N1: U1.D16, Camera.pin4
  N2: U1.D17, Camera.pin3
  N3: Arduino_Ethernet_Shield1.D8, Motion_Detect.pin5
  N4: Arduino_Ethernet_Shield1.D7, Motion_Detect.pin7
  N5: Arduino_Ethernet_Shield1.3V3, Motion_Detect.pin2, Motion_Detect.pin6
  N6: Arduino_Ethernet_Shield1.+5V, Camera.pin1
  N7: Arduino_Ethernet_Shield1.GND, Motion_Detect.pin1, Motion_Detect.pin3, Motion_Detect.pin4, Motion_Detect.pin8, Camera.pin2
