# Fritzing sketch id2665_full_board_0 (saved by Fritzing 0.6.4b)
breadboards: 1

parts:
  XTAL1 = Crystal [frequency="16 Mhz" package=THT]
  C3 = Ceramic Capacitor [capacitance=100nF package="100 mil [THT, multilayer]"]
  IC1 = IC, DIP package, 28 pins [chip_label=IC spacing=300mil]
  R1 = Resistor [tolerance=±5% resistance=10k package=THT]
  Power_plug1 = Power plug
  C6 = Electrolytic Capacitor [capacitance=47µF voltage=25V package="100 mil [THT, electrolytic]"]
  IC3 = IC, DIP package, 8 pins [chip_label=MAX485 spacing=300mil]
  R2 = Resistor [tolerance=±5% resistance=100 package=THT]
  J2 = female pin header, 2 pins [form="♂ (male)"]
  IC4 = IC, DIP package, 16 pins [chip_label=IC spacing=300mil]
  R3 = Resistor [tolerance=±5% resistance=120 package=THT]
  R4 = Resistor [tolerance=±5% resistance=120 package=THT]
  R5 = Resistor [tolerance=±5% resistance=120 package=THT]
  S1 = Pushbutton [package="[THT]"]
  U1 = Optocoupler [package=THT]
  U2 = Optocoupler [package=THT]
  U3 = Optocoupler [package=THT]
  R6 = Resistor [tolerance=±5% resistance=470 package=THT]
  R7 = Resistor [tolerance=±5% resistance=470 package=THT]
  R8 = Resistor [tolerance=±5% resistance=470 package=THT]
  C2 = Ceramic Capacitor [capacitance=22pF package="0805 [SMD, multilayer]"]
  C1 = Ceramic Capacitor [capacitance=22pF voltage=6.3V package="0805 [SMD, multilayer]"]
  D1 = Rectifier Diode [part_number=1N4001 package="300 mil [THT]"]
  C7 = Ceramic Capacitor [capacitance=100nF voltage=25V package="100 mil [THT, multilayer]"]
  C4 = Electrolytic Capacitor [capacitance=47µF voltage=25V package="100 mil [THT, electrolytic]"]
  J4 = screw terminal, 4 pins
  J3 = screw terminal, 8 pins
  J1 = screw terminal, 3 pins
  IC5 = IC, DIP package, 12 pins [chip_label=IC spacing=300mil]
  S7 = Toggle Switch [package=THT]
  S8 = Toggle Switch [package=THT]
  S9 = Toggle Switch [package=THT]
  S10 = Toggle Switch [package=THT]
  LED1 = smd LED [color="Yellow (574nm)" package="0805 [SMD]"]
  R9 = Resistor [tolerance=±5% resistance=1k package="0805 [SMD]"]
  U4 = Voltage Regulator - 5V [package="TO220 [THT]"]
  R10 = Resistor [tolerance=±5% resistance=1k package="0805 [SMD]"]
  LED2 = smd LED [color="Orange (612nm)" package="0805 [SMD]"]
  LED3 = smd LED [color="Orange (612nm)" package="0805 [SMD]"]
  R11 = Resistor [tolerance=±5% resistance=1k package="0805 [SMD]"]
  R12 = Resistor [tolerance=±5% resistance=470 package="0805 [SMD]"]

nets:
  N1: XTAL1.pin_0, IC1.pin9, C1.1
  N2: XTAL1.pin_1, IC1.pin10, C2.1
  GND: C3.0, IC1.pin8, IC1.pin22, Power_plug1.GND, C6.-, IC3.pin5, IC4.pin7, S1.Pin_2, U1.Pin_2, U2.Pin_2, U3.Pin_2, C2.0, C1.0, D1.anode, C7.0, C4.-, J3.pin1, J1.pin3, IC5.pin7, IC5.pin8, IC5.pin9, IC5.pin10, IC5.pin11, IC5.pin12, S10.L2, LED1.cathode, U4.GND, LED2.cathode, LED3.cathode
  5V: C3.1, IC1.pin7, IC1.pin20, R1.Pin_0, C6.+, IC3.pin8, IC4.pin16, D1.cathode, C7.1, J3.pin2, R9.Pin_0, U4.output_voltage
  N3: IC1.pin1, R1.Pin_1, S1.Pin_3, S1.Pin_4
  N4: IC1.pin2, IC3.pin1, R10.Pin_0
  N5: IC1.pin3, IC3.pin4, R11.Pin_0
  N6: IC1.pin4, IC3.pin2, IC3.pin3
  N7: IC1.pin5, IC4.pin14
  N8: IC1.pin6, IC4.pin12
  N9: IC1.pin11, IC4.pin10
  N10: IC1.pin12, R6.Pin_1
  N11: IC1.pin13, R7.Pin_1
  N12: IC1.pin14, R8.Pin_1, R12.Pin_0
  N13: IC1.pin15, S10.COM
  N14: IC1.pin23, IC5.pin6
  N15: IC1.pin24, IC5.pin5
  N16: IC1.pin25, IC5.pin4
  N17: IC1.pin26, IC5.pin3
  N18: IC1.pin27, IC5.pin2
  N19: IC1.pin28, IC5.pin1
  N20: Power_plug1.VCC, C4.+, U4.input_voltage
  N21: IC3.pin6, R2.Pin_1, J1.pin2
  N22: IC3.pin7, J2.pin2, J1.pin1
  N23: R2.Pin_0, J2.pin1
  N24: IC4.pin1, R3.Pin_0, J3.pin8
  N25: IC4.pin2, R3.Pin_1, J3.pin7
  N26: IC4.pin3, R4.Pin_0, J3.pin6
  N27: IC4.pin4, R4.Pin_1, J3.pin5
  N28: IC4.pin5, R5.Pin_0, J3.pin4
  N29: IC4.pin6, R5.Pin_1, J3.pin3
  N30: U1.Pin_1, R6.Pin_0
  N31: U1.Pin_4, U2.Pin_4, S7.L1
  N32: U1.Pin_5, J4.pin4, S8.L2
  N33: U2.Pin_1, R7.Pin_0
  N34: U2.Pin_5, J4.pin3, S9.L2
  N35: U3.Pin_1, R8.Pin_0, R12.Pin_1
  N36: U3.Pin_4, J4.pin1, S7.COM
  N37: U3.Pin_5, J4.pin2
  N38: S7.L2, S8.COM, S9.COM
  N39: LED1.anode, R9.Pin_1
  N40: R10.Pin_1, LED2.anode
  N41: LED3.anode, R11.Pin_1
