# Fritzing sketch id2666_Helmet_0 (saved by Fritzing 0.9.2b)
circuit board: 8.46667cm x 5.64444cm
breadboards: 1

parts:
  Part1 = Arduino Uno (Rev3)
  Part2 = Triple Axis Accelerometer Breakout - ADXL335
  R1 = Resistor [tolerance=±5% resistance=220 package="2512 [SMD]"]
  R2 = Resistor [tolerance=±5% resistance=150 package="2512 [SMD]"]
  R3 = Resistor [tolerance=±5% resistance=220 package="2512 [SMD]"]
  LED1 = LED - 5mm [color="Red (633nm)" package="5 mm [THT]"]
  LED2 = LED - 5mm [color="Yellow (592nm)" package="5 mm [THT]"]
  LED3 = LED - 5mm [color="Yellow (585nm)" package="5 mm [THT]"]
  BAT1 = BC9VPC [package=bc9vpc]
  Power_plug1 = Power plug

nets:
  N1: Part1.A0, Part2.XOUT
  N2: Part1.A1, Part2.YOUT
  N3: Part1.A2, Part2.ST, Part2.ZOUT
  N4: Part1.D11_PWM/MOSI, R3.Pin_0
  N5: Part1.D12/MISO, R2.Pin_1
  N6: Part1.D13/SCK, R1.Pin_0
  3V3: Part1.3V3, Part2.VCC
  GND: Part1.GND, Part2.GND, LED1.cathode, LED2.cathode, LED3.cathode
  N7: R1.Pin_1, LED2.anode
  N8: R2.Pin_0, LED3.anode
  N9: R3.Pin_1, LED1.anode
  N10: BAT1.V+, Power_plug1.GND
  N11: BAT1.V-, Power_plug1.VCC
