# Fritzing sketch id2667_Schematic_0 (saved by Fritzing 0.9.3b)
breadboards: 1

parts:
  Part1 = Arduino Uno (Rev3)
  U1 = MLX90614 [package=to-39]  # not connected
  R1 = Trimmer Potentiometer [maximum_resistance=10kΩ package=THT]
  U2 = LCD-16X2 [package=lcd-16x2]
  LED1 = smd LED [color="Red (633nm)" package="0603 [SMD]"]
  R2 = Resistor [tolerance=±5% resistance=220 package="1206 [SMD]"]
  J1 = Piezo Speaker

nets:
  N1: Part1.D10_PWM/SS, J1.pin2
  N2: Part1.D11_PWM/MOSI, U2.E
  N3: Part1.D12/MISO, U2.RS
  N4: Part1.D13/SCK, LED1.cathode
  GND: Part1.GND, R1.leg1, U2.VSS, U2.R_W, U2.K, LED1.anode
  N5: Part1.D2, U2.DB7
  N6: Part1.D3_PWM, U2.DB6
  N7: Part1.D4, U2.DB5
  N8: Part1.D5_PWM, U2.DB4
  5V: Part1.5V, R1.leg2, U2.VDD, R2.Pin_0, J1.pin1
  N9: R1.wiper, U2.VO
  N10: U2.A, R2.Pin_1

notes:
  GND - OUT - VCC
