# Fritzing sketch id2668_Motion_Sensing_Alarm_with_Keypad_and_Password_0 (saved by Fritzing 0.9.3b)
breadboards: 1

parts:
  Part1 = Arduino Uno (Rev3)
  R1 = Resistor [tolerance=±5% resistance=330 package=THT]
  R2 = Resistor [tolerance=±5% resistance=330 package=THT]
  R3 = Resistor [tolerance=±5% resistance=330 package=THT]
  LED1 = LED - 3mm [color="Red (633nm)" package="3 mm [THT]"]
  LED2 = LED - 3mm [color="Yellow (595nm)" package="3 mm [THT]"]
  LED3 = LED - 3mm [color="Green (570nm)" package="3 mm [THT]"]
  Keypad4x1 = Keypad4x4
  Part3 = PIR D-SUN HC-SR501
  Part2 = KY-012

nets:
  N1: Part1.A0, R3.Pin_1
  N2: Part1.A1, R2.Pin_1
  N3: Part1.A2, R1.Pin_1
  N4: Part1.A3, Part3.connector1
  N5: Part1.D8, Keypad4x1.connector1
  N6: Part1.D9_PWM, Keypad4x1.connector0
  N7: Part1.D10_PWM/SS, Part2.connector0
  N8: Part1.GND, LED1.cathode, LED2.cathode, LED3.cathode, Part3.connector2, Part2.connector2
  N9: Part1.D2, Keypad4x1.connector8
  N10: Part1.D3_PWM, Keypad4x1.connector7
  N11: Part1.D4, Keypad4x1.connector6
  N12: Part1.D5_PWM, Keypad4x1.connector5
  N13: Part1.D6_PWM, Keypad4x1.connector4
  N14: Part1.D7, Keypad4x1.connector2
  N15: Part1.5V, Part3.connector0, Part2.connector3
  N16: R1.Pin_0, LED1.anode
  N17: R2.Pin_0, LED2.anode
  N18: R3.Pin_0, LED3.anode
