# Fritzing sketch id2669_moto_moped_speed_limiter_0 (saved by Fritzing 0.9.3b)
breadboards: 1

parts:
  IC1 = Voltage Regulator [package=to-220-alt]
  Part1 = Arduino Nano (Rev3.0)
  LED1 = smd LED [color="Green (570nm)" package="1206 [SMD]"]
  R1 = Resistor [tolerance=±5% resistance=380 package=THT]
  S1 = Pushbutton [package="[THT]"]
  C1 = Ceramic Capacitor [capacitance=10nF package="100 mil [THT, multilayer]"]
  S2 = Pushbutton [package=THT]
  R2 = Rotary Potentiometer (Small) [maximum_resistance=100kΩ package=THT]
  Q1 = PNP-Transistor [package="TO92 [THT]"]
  R3 = Resistor [tolerance=±5% resistance=6.8k package=THT]
  U1 = TRIAC [package=to-92]
  R4 = Resistor [tolerance=±5% resistance=380 package=THT]

nets:
  GND: IC1.GND, Part1.GND, R1.Pin_0, C1.1, R2.leg2, Q1.C, U1.M1
  N1: IC1.OUT, Part1.VIN
  N2: Part1.D2, Q1.B, R3.Pin_1
  N3: Part1.D6, S1.Pin_3, S1.Pin_4, C1.0
  N4: Part1.D12/MISO, LED1.anode
  N5: Part1.5V, R2.leg1, Q1.E
  N6: Part1.A0, R2.wiper
  N7: LED1.cathode, R1.Pin_1
  N8: S1.Pin_1, S1.Pin_2, S2.leg1
  N9: U1.M2, R4.Pin_0

notes:
  +12V from moto (regulator)
  GND
  engine off button (hijack/replace)
  triple-click, turn off speed limiter
  magnetic hall sensor (TLE4905L)
  Moto front wheel (magnetic speed meter)
  TIC206D
  Ignition coil input signal
  Signal to ground prevent spark
