# Fritzing sketch id2670_arduino_motor_cc_med_potencia_0 (saved by Fritzing 0.7.10b)
breadboards: 1

parts:
  R1 = Rotary Potentiometer (Large) [maximum_resistance=10kΩ package=THT]
  Arduino1 = Arduino
  D1 = Rectifier Diode [part_number=1N4001 package="300 mil [THT]"]
  VCC1 = 4 x AAA Battery Mount
  Q1 = NPN-Transistor [package="TO92 [THT]"]
  M1 = DC Motor
  LED1 = LED - 5mm [color="Green (555nm)" package="5 mm [THT]"]
  LED2 = LED - 5mm [color="Yellow (585nm)" package="5 mm [THT]"]
  LED3 = LED - 5mm [color="Red (633nm)" package="5 mm [THT]"]
  R2 = Resistor [tolerance=±5% resistance=100 package=THT]
  R3 = Resistor [tolerance=±5% resistance=100 package=THT]
  R4 = Resistor [tolerance=±5% resistance=100 package=THT]

nets:
  N1: R1.leg1, Arduino1.GND, D1.anode, VCC1.-, Q1.C, LED1.cathode, LED2.cathode, LED3.cathode
  N2: R1.wiper, Arduino1.A0
  N3: R1.leg2, Arduino1.+5V
  N4: Arduino1.D9, Q1.E
  N5: Arduino1.D4, LED3.anode, R4.Pin_0, R4.Pin_1
  N6: Arduino1.D3, LED2.anode, R3.Pin_0, R3.Pin_1
  N7: Arduino1.D2, LED1.anode, R2.Pin_0, R2.Pin_1
  N8: D1.cathode, Q1.B, M1.pin_2
  N9: VCC1.+, M1.pin_1
