# Fritzing sketch id2671_Motor_CC_no_Arduino_com_ponte_H_dupla_0 (saved by Fritzing 0.7.11b)
breadboards: 1

parts:
  S1 = Toggle Switch [package=THT]
  IC1 = H-Bridge [package=THT]
  Arduino1 = Arduino
  M1 = DC Motor
  VCC1 = 4 x AAA Battery Mount
  R1 = Rotary Potentiometer (Large) [maximum_resistance=100kΩ package=THT]
  R2 = Resistor [tolerance=±5% resistance=10k package=THT]

nets:
  N1: S1.L1, IC1.VCC1, Arduino1.+5V, R1.leg2
  N2: S1.COM, Arduino1.D2, R2.Pin_0
  N3: IC1.1_2EN, Arduino1.D9
  N4: IC1.1A, Arduino1.D3
  N5: IC1.1Y, M1.pin_1
  GND1: IC1.GND1, IC1.GND2, IC1.GND3, IC1.GND4, Arduino1.GND, VCC1.-, R1.leg1, R2.Pin_1
  N6: IC1.2Y, M1.pin_2
  N7: IC1.2A, Arduino1.D4
  N8: IC1.VCC2, VCC1.+
  N9: Arduino1.A0, R1.wiper
