# Fritzing sketch id2673_motorL293D2layers_0 (saved by Fritzing 0.9.1b)
circuit board: 3.05428cm x 3.39675cm
breadboards: 1

parts:
  L293D = L293D [package=THT]
  +_1_2_3_4_- = female pin header, 6 pins [form="♀ (female)"]
  1_2_3_4 = female pin header, 4 pins [form="♀ (female)"]

nets:
  N1: L293D.Enable_1, L293D.+Vmotor, L293D.Enable_2, L293D.+V, +_1_2_3_4_-.pin1
  N2: L293D.In_1, +_1_2_3_4_-.pin2
  N3: L293D.Out_1_(_Controlled_by_Enable_1_), 1_2_3_4.pin4
  N4: L293D.0V, +_1_2_3_4_-.pin6
  N5: L293D.Out_2_(_Controlled_by_Enable_1_), 1_2_3_4.pin3
  N6: L293D.In_2, +_1_2_3_4_-.pin3
  N7: L293D.In_3, +_1_2_3_4_-.pin5
  N8: L293D.Out_3_(_Controlled_by_Enable_2_), 1_2_3_4.pin2
  N9: L293D.Out_4_(_Controlled_by_Enable_2_), 1_2_3_4.pin1
  N10: L293D.In_4, +_1_2_3_4_-.pin4

notes:
  motor
  input
  librepensante.org
  2015
