# Fritzing sketch id2674_motorcd_0 (saved by Fritzing 0.7.9b)
breadboards: 1

parts:
  L293D = L293D [package=THT]
  VCC = female pin header, 2 pins [form="♀ (female)"]
  motor2 = female pin header, 2 pins [form="♀ (female)"]
  part = shrouded pin header, 10 pins [form="♂ (shrouded male)"]  # not connected
  motor1 = female pin header, 2 pins [form="♀ (female)"]
  part_2 = female pin header, 2 pins [form="♀ (female)"]  # not connected
  part_3 = female pin header, 2 pins [form="♀ (female)"]  # not connected
  part_4 = 555 Timer [package="SO8 [SMD]"]  # not connected
  attiny45 = 555 Timer [package="DIP8 [THT]"]
  part_5 = Rotary Potentiometer (Small) [maximum_resistance=100kΩ]  # not connected
  R2 = Rotary Potentiometer (Large) [package=THT]
  S1 = Toggle Switch [package=THT]

nets:
  N1: L293D.Enable_1, L293D.+Vmotor, L293D.Enable_2, L293D.+V, VCC.pin2, attiny45.Vcc_Supply_Voltage, R2.leg2
  N2: L293D.In_1, attiny45.Output
  N3: L293D.Out_1_(_Controlled_by_Enable_1_), motor1.pin1
  N4: L293D.0V, VCC.pin1, S1.L1
  N5: L293D.Out_2_(_Controlled_by_Enable_1_), motor1.pin2
  N6: L293D.In_2, attiny45.Control_Voltage
  N7: L293D.Out_3_(_Controlled_by_Enable_2_), motor2.pin2
  N8: L293D.Out_4_(_Controlled_by_Enable_2_), motor2.pin1
  N9: attiny45.Trigger, R2.wiper
  N10: attiny45.Reset, R2.leg1, S1.COM
