# Fritzing sketch id2676_arduino_DUE_y_stepper_0 (saved by Fritzing 0.9.0b)

parts:
  Parte1 = Arduino Due (Rev2b)
  M2 = Stepper Motor - Bipolar
  MD09B1 = A4988 Stepper Motor Driver Carrier

nets:
  N1: Parte1.D11_PWM, MD09B1.DIR
  N2: Parte1.D12_PWM, MD09B1.STEP
  N3: Parte1.D13_PWM, MD09B1.RESET, MD09B1.SLEEP
  N4: Parte1.D2_PWM, MD09B1.Enable
  N5: Parte1.D3_PWM, MD09B1.MS1
  N6: Parte1.D4_PWM/SS1, MD09B1.MS2
  N7: Parte1.D5_PWM, MD09B1.MS3
  N8: Parte1.GND, MD09B1.GROUND#147
  N9: M2.A, MD09B1.OUT_2B
  N10: M2.C, MD09B1.OUT_2A
  N11: M2.B, MD09B1.OUT_1A
  N12: M2.D, MD09B1.OUT_1B

notes:
  12 Voltios de mi Fuente de alimentacion de un PC viejo.
  (-) (+)
  5 Voltios de mi Fuente de alimentacion de un PC viejo.
  (-) (+)
  //
  // Probando la velocidad de mi motor paso a paso...
  //
  ind lentitud = 200;
  int enable = 2;
  int MS1 = 3;
  int MS2 = 4;
  int MS3 = 5;
  int direccion = 11;
  int step = 12;
  int reset = 13;
  void setup() {
  pinMode(enable, OUTPUT);
  pinMode(MS1, OUTPUT);
  pinMode(MS2, OUTPUT);
  pinMode(MS3, OUTPUT);
  pinMode(direccion, OUTPUT);
  pinMode(steps, OUTPUT);
  pinMode(reset, OUTPUT);
  digitalWrite(enable, LOW);
  digitalWrite(MS1, HIGH);
  digitalWrite(MS2, HIGH);
  digitalWrite(MS3, HIGH);
  digitalWrite(direccion, LOW);
  digitalWrite(reset, HIGH);
  }
  void loop() {
  digitalWrite(step, LOW);
  delayMicroseconds(1);
  digitalWrite(step, HIGH);
  delayMicroseconds(lentitud);
  }
