# Fritzing sketch id2678_PlacaTeste2_0 (saved by Fritzing 0.9.2b)
breadboards: 1

parts:
  IC1 = ULN2003A [package="SO16 [SMD]"]
  USB1 = Wiring USB Adapter
  VCC1 = Battery block 9V
  M1 = Stepper Motor - Unipolar

nets:
  N1: IC1.In_1, USB1.CTS
  N2: IC1.In_2, USB1.DSR
  N3: IC1.In_3, USB1.RTS
  N4: IC1.In_4, USB1.DTR
  N5: IC1.0V, USB1.GND, VCC1.-
  N6: IC1.COM_-_Common, USB1.5V, VCC1.+, M1.COMMON_2, M1.D
  N7: IC1.Out_4, M1.B
  N8: IC1.Out_3, M1.C
  N9: IC1.Out_2, M1.COMMON_1
  N10: IC1.Out_1, M1.A
