# Fritzing sketch id267_Untitled_Sketch_ultrasonic_0 (saved by Fritzing 0.9.3b)
breadboards: 1

parts:
  Composant1 = SRF05 Ultrasonic Rangefinder
  Composant2 = Arduino Uno (Rev3)
  SPKR1 = Loudspeaker
  R1 = Resistor [tolerance=±5% resistance=220 package=THT]

nets:
  N1: Composant1.connector8, Composant2.VIN
  N2: Composant1.connector9, Composant2.D6_PWM
  N3: Composant1.connector10, Composant2.D7
  N4: Composant2.D8, R1.Pin_1
  N5: Composant2.GND, SPKR1.pin1
  N6: SPKR1.pin2, R1.Pin_0
