# Fritzing sketch id2680_MotorcyclePanel_0 (saved by Fritzing 0.7.4b)
breadboards: 1

parts:
  Nano1 = Arduino Nano v2.3
  LCD1 = LCD screen
  U1 = mystery part, 3 pins [chip_label=? spacing=300mil]
  Part1 = Triple Axis Magnetometer - HMC5883 Breakout
  Part2 = Bluetooth Mate Silver
  R1 = Resistor [tolerance=±5% resistance=4.7k package=THT]
  R2 = Resistor [tolerance=±5% resistance=4.7k package=THT]
  R3 = Trimmer Potentiometer [maximum_resistance=10kΩ package=THT]

nets:
  GND: Nano1.GND, LCD1.VSS, LCD1.R/W, LCD1.LED-, U1.pin1, Part1.GND, Part2.GND, R3.leg2
  N1: Nano1.D4, Part2.RX_5V
  N2: Nano1.D5, Part2.TX_5V
  N3: Nano1.D6, U1.pin2
  N4: Nano1.D7, LCD1.RS
  N5: Nano1.D8, LCD1.E
  N6: Nano1.D9, LCD1.DB4
  N7: Nano1.D10, LCD1.DB5
  N8: Nano1.D11, LCD1.DB6
  N9: Nano1.D12, LCD1.DB7
  N10: Nano1.A5, Part1.SCL, R1.Pin_1
  N11: Nano1.A4, Part1.SDA, R2.Pin_1
  VCC: Nano1.+5V, LCD1.VDD, LCD1.LED+, U1.pin3, Part1.VCC, Part2.VCC, R1.Pin_0, R2.Pin_0, R3.leg1
  N12: LCD1.V0, R3.wiper
