# Fritzing sketch id2681_Lightning_Trigger (saved by Fritzing 0.6.3b)
breadboards: 1

parts:
  R1 = Resistor [tolerance=±5% resistance=220 package=THT]
  Arduino1 = Arduino
  IR_Transmitter = LED - 5mm [color="Infrared (940nm)" part_number=276-0142 package="5 mm [THT]"]
  Photosresistor = Photocell (LDR) [package=THT]

nets:
  N1: R1.Pin_0, Arduino1.A0, Photosresistor.pin_1
  N2: R1.Pin_1, Arduino1.GND, IR_Transmitter.cathode
  N3: Arduino1.D13, IR_Transmitter.anode
  N4: Arduino1.+5V, Photosresistor.pin_0
