# Fritzing sketch id2681_shayGear_0 (saved by Fritzing 0.7.7b)
breadboards: 1
stripboards: 3

parts:
  U1 = atmega168 [package=dip]
  R1 = Resistor [tolerance=±5% resistance=10k package=THT]
  S1 = Pushbutton [package="[THT]"]
  R2 = Resistor [tolerance=±5% resistance=220 package=THT]
  LED1 = LED - 5mm [color="Green (570nm)" package="5 mm [THT]"]
  LED2 = LED - 5mm [color="Red (633nm)" package="5 mm [THT]"]
  R3 = Resistor [tolerance=±5% resistance=220 package=THT]
  Q2 = Basic FET P-Channel [package="TO220 [THT]"]
  C5 = Electrolytic Capacitor [capacitance=10µF package="100 mil [THT, electrolytic]"]
  C6 = Electrolytic Capacitor [capacitance=10µF package="100 mil [THT, electrolytic]"]
  IC1 = Hex Inverter Schmitt Trigger SN74HC14 [package="DIP (Dual Inline)"]
  Up1 = Pushbutton [package="[THT]"]
  Down1 = Pushbutton [package="[THT]"]
  C9 = Electrolytic Capacitor [capacitance=10µF package="100 mil [THT, electrolytic]"]
  C10 = Electrolytic Capacitor [capacitance=10µF package="100 mil [THT, electrolytic]"]
  R4 = Resistor [tolerance=±5% resistance=10k package=THT]
  R5 = Resistor [tolerance=±5% resistance=10k package=THT]
  C11 = Tantalum Capacitor [capacitance=100nF package="100 mil [THT, tantalum]"]
  C12 = Tantalum Capacitor [capacitance=100nF package="100 mil [THT, tantalum]"]
  Fuse2 = Fuse with Handler [part_number=Htc-15m]
  C13 = Ceramic Capacitor [capacitance=100nF package="100 mil [THT, multilayer]"]
  C14 = Ceramic Capacitor [capacitance=100nF package="100 mil [THT, multilayer]"]
  XTAL2 = Crystal [frequency="16 Mhz" package=THT]
  J1 = screw terminal, 3 pins
  Q3 = Basic FET P-Channel [package="TO220 [THT]"]
  C15 = Electrolytic Capacitor [capacitance=10µF package="100 mil [THT, electrolytic]"]
  C16 = Electrolytic Capacitor [capacitance=10µF package="100 mil [THT, electrolytic]"]
  J2 = screw terminal, 3 pins
  7_Segment1 = 7 Segment Display

nets:
  N1: U1.RESET, R1.Pin_0, S1.Pin_1, S1.Pin_2
  N2: U1.D2, IC1.3Y
  N3: U1.D3_(PWM), IC1.1Y
  N4: U1.D4, IC1.2Y
  VCC: U1.VCC, U1.AVCC, R1.Pin_1, R2.Pin_0, Q2.source, C5.+, IC1.VCC, R4.Pin_1, R5.Pin_1, C11.+, J1.pin1
  N5: U1.GND#7, S1.Pin_3, S1.Pin_4, LED1.cathode, R3.Pin_1, Q2.drain, C5.-, C6.+, IC1.GND, C12.-, C12.+, C13.0, C14.1, J1.pin2, Q3.drain, C15.-, C16.+, J2.pin2, 7_Segment1.common_anode
  N6: U1.XLAT1, C14.0, XTAL2.pin_0
  N7: U1.XLAT2, C13.1, XTAL2.pin_1
  N8: U1.D5_(PWM), 7_Segment1.Segment_G
  N9: U1.D6_(PWM), 7_Segment1.Segment_F
  N10: U1.D7, 7_Segment1.Segment_E
  N11: U1.D8, 7_Segment1.Segment_D
  N12: U1.D9_(PWM), 7_Segment1.Segment_DP
  N13: U1.D10_(PWM), 7_Segment1.Segment_C
  N14: U1.D11_(PWM), 7_Segment1.Segment_B
  N15: U1.D12, 7_Segment1.Segment_A
  N16: U1.D13, LED2.cathode
  N17: U1.GND#21, C11.-
  N18: R2.Pin_1, LED1.anode
  N19: LED2.anode, R3.Pin_0
  N20: C6.-, J1.pin3
  N21: IC1.1A, Up1.Pin_3, Up1.Pin_4, C10.+
  N22: IC1.2A, Down1.Pin_3, Down1.Pin_4, C9.+
  N23: IC1.3A, Q3.source, C15.+, J2.pin1
  N24: Up1.Pin_1, Up1.Pin_2, C10.-, R4.Pin_0
  N25: Down1.Pin_1, Down1.Pin_2, C9.-, R5.Pin_0
  N26: Fuse2.Connector2, C16.-, J2.pin3

notes:
  To Neutral light
  To Main power
  Single board (both entries)
  Single board 7seg
  Single board all the rest
