# Fritzing sketch id2682_BlowerTestBoard_0 (saved by Fritzing 0.8.7b)
circuit board: 8.46667cm x 5.64444cm
breadboards: 1

parts:
  Part1 = Arduino Micro (Rev3)
  R1 = Trimmer Potentiometer [maximum_resistance=10kΩ package=THT]
  TRINKET1 = Trinket_5V
  R2 = Trimmer Potentiometer [maximum_resistance=10kΩ package=THT]
  J3 = Basic Servo

nets:
  GND: Part1.GND, R1.leg2, TRINKET1.connector2, R2.leg2, J3.gnd
  N1: Part1.D9_PWM/A9, Part1.D10_PWM/A10, TRINKET1.connector4
  N2: Part1.5V, R1.leg1, TRINKET1.connector1, R2.leg1
  N3: Part1.A0, R2.wiper
  N4: R1.wiper, TRINKET1.connector7
  N5: TRINKET1.connector9, J3.pulse

notes:
  Trim pot RI Throttle
  Trim pot R2
  Crank
  USB micro connector
  for Power input/code
  <<-----------------
