# Fritzing sketch id2683_motorshield_fan_ldr_pots_0 (saved by Fritzing 0.7.11b)
breadboards: 1

parts:
  R1 = Rotary Potentiometer (Small) [maximum_resistance=10kΩ]
  R2 = Rotary Potentiometer (Small) [maximum_resistance=100kΩ]
  U1 = Arduino Mega
  J1 = Piezo Speaker
  LED1 = LED - 5mm [color="Red (633nm)" package="5 mm [THT]"]
  LED2 = LED - 5mm [color="Red (633nm)" package="5 mm [THT]"]
  M1 = DC Motor  # not connected
  R3 = Photocell (LDR) [package=THT]
  R4 = Resistor [tolerance=±5% resistance=220 package=THT]
  R5 = Resistor [tolerance=±5% resistance=220 package=THT]
  R6 = Resistor [tolerance=±5% resistance=220 package=THT]

nets:
  N1: R1.leg1, R2.leg1, U1.GND, J1.pin1, R4.Pin_1, R5.Pin_1, R6.Pin_1
  N2: R1.wiper, U1.A8
  N3: R1.leg2, R2.leg2, U1.+5V, R3.pin_0
  N4: R2.wiper, U1.A9
  N5: U1.A5, R3.pin_1, R4.Pin_0
  N6: U1.D22, LED1.cathode
  N7: U1.D23, LED2.cathode
  N8: U1.D49, J1.pin2
  N9: LED1.anode, R6.Pin_0
  N10: LED2.anode, R5.Pin_0

notes:
  motor pins are attached to
  channel A on motorshield
