# Fritzing sketch id2685_arduino_ros_0 (saved by Fritzing 0.9.3b)
breadboards: 1

parts:
  パーツ1 = Arduino Nano (Rev3.0) (ICSP)
  R1 = Resistor [tolerance=±5% resistance=10k package=THT]
  R2 = Resistor [tolerance=±5% resistance=10k package=THT]
  Q1 = MOSFET-NCHANNEL [package=to220v]
  Q2 = MOSFET-NCHANNEL [package=to220v]
  U1 = BATTERY-2 [package=battery-aaa]
  M1 = DC Motor
  M2 = DC Motor

nets:
  N1: パーツ1.GND, Q1.S, Q2.S, U1.-1
  N2: パーツ1.D2, R2.Pin_0
  N3: パーツ1.D12/MISO, R1.Pin_1
  N4: R1.Pin_0, Q2.G
  N5: R2.Pin_1, Q1.G
  N6: Q1.D, M1.pin_2
  N7: Q2.D, M2.pin_2
  N8: U1.+1, M1.pin_1, M2.pin_1
