# Fritzing sketch id2686_ChiefV1.0(GALILEO)_0 (saved by Fritzing 0.9.3b)
breadboards: 1

parts:
  Componente1 = Intel Galileo
  R1 = Resistor [tolerance=±5% resistance=220 package=THT]
  LED1 = LED - 5mm [color="Red (633nm)" package="5 mm [THT]"]
  J1 = Infrared Proximity Sensor

nets:
  N1: Componente1.D9_PWM, LED1.anode
  N2: Componente1.GND, R1.Pin_1, J1.Vout
  N3: Componente1.D7, J1.Vcc
  N4: Componente1.vin-2, J1.GND
  N5: R1.Pin_0, LED1.cathode
