# Fritzing sketch id2687_MoviePropSchematics_0 (saved by Fritzing 0.9.2b)
breadboards: 1

parts:
  Part1 = Arduino Uno (Rev3)
  J1 = Basic Force Sensing Resistor (FSR) [package=THT]
  J2 = Basic Force Sensing Resistor (FSR) [package=THT]
  J3 = Basic Force Sensing Resistor (FSR) [package=THT]
  R1 = Resistor [tolerance=±5% resistance=220 package=THT]
  R2 = Resistor [tolerance=±5% resistance=220 package=THT]
  R3 = Resistor [tolerance=±5% resistance=220 package=THT]
  LED1 = RGB LED (com. cathode, rgb) [package="5 mm [THT]"]
  R4 = Resistor [tolerance=±5% resistance=220 package=THT]
  R5 = Resistor [tolerance=±5% resistance=220 package=THT]
  R6 = Resistor [tolerance=±5% resistance=220 package=THT]

nets:
  N1: Part1.A0, J3.pin_0, R1.Pin_0
  N2: Part1.A1, J1.pin_0, R2.Pin_0
  N3: Part1.A2, J2.pin_0, R3.Pin_0
  N4: Part1.D9_PWM, LED1.red_anode, R4.Pin_0
  N5: Part1.D10_PWM/SS, LED1.green_anode, R5.Pin_0
  N6: Part1.D11_PWM/MOSI, LED1.blue_anode, R6.Pin_0
  N7: Part1.GND, R2.Pin_1, R3.Pin_1
  N8: Part1.5V, J1.pin_1, J2.pin_1, J3.pin_1, LED1.common_cathode
