# Fritzing sketch id2689_servo_and_sonic_0 (saved by Fritzing 0.9.0b)
breadboards: 1

parts:
  Part3 = SRF05 Ultrasonic Rangefinder
  Part4 = Arduino Uno (Rev3) - ICSP
  J1 = Basic Servo

nets:
  5V: Part3.connector8, Part4.5V, J1.vcc
  N1: Part3.connector9, Part4.D9_PWM
  N2: Part3.connector10, Part4.D10_PWM/SS
  GND: Part3.connector11, Part4.GND, J1.gnd
  N3: Part4.ICSP_MISO, Part4.D12/MISO, J1.pulse

notes:
  Oliver Sumabat
  Sonic
  Servo
  Arduino
