# Fritzing sketch id268_AI_Thinker_to_4_Relay_Modules_0 (saved by Fritzing 0.9.1b)
circuit board: 8.46667cm x 5.64444cm

parts:
  U1 = esp12 [part_number=ESP8266]
  Relay = JTRON 1CH RELAY
  Part2 = JTRON 1CH RELAY
  Part3 = JTRON 1CH RELAY
  Part4 = JTRON 1CH RELAY
  VCC2 = 4 x AAA Battery Mount  # not connected
  5Vreg = DC-DC 5v (top)
  VCC1 = 4 x AAA Battery Mount

nets:
  N1: U1.connector3, Relay.connector4
  N2: U1.connector5, Part2.connector4
  N3: U1.connector7, VCC1.-
  N4: U1.connector13, Part4.connector4
  N5: U1.connector14, Part3.connector4
  N6: U1.connector18, VCC1.+
  N7: Relay.connector3, Relay.connector5, Part2.connector5, Part3.connector5, Part4.connector0, Part4.connector2, Part4.connector5, 5Vreg.connector4
