# Fritzing sketch id2690_gps_mower_0 (saved by Fritzing 0.7.12b)
breadboards: 1

parts:
  Arduino_Ethernet_Shield1 = Arduino Ethernet Shield  # not connected
  Arduino1 = Arduino
  MD03A1 = Dual VNH2SP30 Motor Driver [part_number=MD03A]
  M2 = Stepper Motor - Bipolar
  Part1 = Arduino GPS Shield  # not connected
  U3 = XBee
  Arduino2 = Arduino  # not connected
  ANT1 = Antenna  # not connected
  ANT2 = Antenna  # not connected
  Part2 = Arduino Xbee Libellium Shield  # not connected
  Part3 = Arduino Xbee Libellium Shield
  M3 = Stepper Motor - Bipolar
  U4 = XBee  # not connected
  U5 = XBee  # not connected
  J1 = Basic Servo

nets:
  N1: Arduino1.D10, J1.pulse
  +5V: Arduino1.+5V, J1.vcc
  GND: Arduino1.GND, J1.gnd
  N2: MD03A1.OUT_1A, M2.A
  N3: MD03A1.OUT_1B, M2.B
  N4: MD03A1.OUT_2A, M3.A
  N5: MD03A1.OUT_2B, M3.B
  N6: MD03A1.GND, M2.C, M2.D, M3.C, M3.D
  N7: U3.VCC, Part3.DIN
  N8: U3.pin2, Part3.4
  N9: U3.pin3, Part3.RST
  N10: U3.pin4, Part3.PWM0
  N11: U3.pin5, Part3.PWM1
  N12: U3.pin6, Part3.8
  N13: U3.pin7, Part3.9
  N14: U3.pin8, Part3.GND

notes:
  transmitter
  receiver
  receiver
  microcontroller
  gps module
  zigbee 1
  zigbee 2
  transmitter microcontroller
  ethernet shield;
  we use this shield to have full control in long distances throught internet conection in home using an android app in our cellphone
  throtle servo
  this servo can reduce or increase the gas amount to the carburator of the mower
  motor shield;
  this is used to andle high power devices and can be set it up togheter with the microcontroller
  basically we have to use the zigbees to communicate the coordinates between our computer or cellphone received by the gps, escentially zigbees keep communicated back and forward at all the time
  as you see sevda the order of the pins between the shields and the micro controller are all ready for just plug on. just we need to add an starting motor for the engine and write the program
