# Fritzing sketch id2691_Final_Projec___MP3_Shield,_LCD,_Buttons_0 (saved by Fritzing 0.8.7b)
breadboards: 1

parts:
  U1 = LCD-16X2 [package=lcd-16x2]
  R1 = Resistor [tolerance=±1% package="0402 [SMD]"]
  Part1 = Arduino Uno (Rev3)  # not connected
  Part2 = Arduino MP3 Player Shield
  R2 = Resistor [tolerance=±5% resistance=47k package=THT]
  R3 = Resistor [tolerance=±5% resistance=47k package=THT]
  S1 = Pushbutton [package="[THT]"]
  S2 = Pushbutton [package="[THT]"]
  S3 = Pushbutton [package="[THT]"]
  S4 = Pushbutton [package="[THT]"]
  R4 = Resistor [tolerance=±5% resistance=10k package=THT]
  R5 = Resistor [tolerance=±5% resistance=10k package=THT]
  R6 = Resistor [tolerance=±5% resistance=10k package=THT]
  R7 = Resistor [tolerance=±5% resistance=10k package=THT]

nets:
  VSS: U1.VSS, U1.R_W, R1.Pin_0, Part2.GND, R2.Pin_1, S1.Pin_3, S1.Pin_4, S2.Pin_3, S2.Pin_4, S3.Pin_3, S3.Pin_4, S4.Pin_3, S4.Pin_4
  VDD: U1.VDD, U1.A, Part2.VCC, R4.Pin_1, R5.Pin_1, R6.Pin_1
  N1: U1.VO, R1.Pin_1
  N2: U1.RS, Part2.A0
  N3: U1.E, Part2.A1
  N4: U1.DB4, Part2.A2
  N5: U1.DB5, Part2.A3
  N6: U1.DB6, Part2.A4
  N7: U1.DB7, Part2.A5
  N8: U1.K, R3.Pin_0
  N9: Part2.D5, S2.Pin_1, S2.Pin_2, R5.Pin_0
  N10: Part2.D10, S1.Pin_1, S1.Pin_2, R4.Pin_0
  N11: Part2.RX, S4.Pin_1, S4.Pin_2, R7.Pin_0
  N12: Part2.TX, S3.Pin_1, S3.Pin_2, R6.Pin_0
  N13: R2.Pin_0, R3.Pin_1

notes:
  ( (Key) LCD Pin (#)x - (to) y)
  1 - Ground
  2 - 5V
  3 - 2.2K Resistor to Ground
  4 - Analog Pin 0
  5 - Ground
  6- Analog Pin 1
  7 through 10 are not used
  11 - Analog Pin 2
  12 - Analog Pin 3
  13 - Analog Pin 4
  14 - Analog Pin 5
  15 - 5V
  16 - 47K (Yellow/Purple/Black) Resistor to 47K (Yellow/Purple/Black) Resistor to Ground
  ( (Key) Step (#)x - y)
  1. Have buttons cross breadboard
  2. Left pin of button to ground, right pin of button to 10k resistor to 5V, and to pin on Arduino board
  3. Can only use Arduino digital pins 10,5,1,0 with Sparkfun MP3 shield on
  4. S1 - Digital Pin 10
  5. S2 - Digital Pin 5
  6. S3 - Digital Pin 1
  7. S4 - Digital Pin 0
