# Fritzing sketch id2692_DoorBell_0 (saved by Fritzing 0.9.0b)
circuit board: 6.88566cm x 5.36311cm
breadboards: 1

parts:
  S1 = Pushbutton [package="[THT]"]
  U1 = Arduino Uno (Rev3)
  SPKR1 = Loudspeaker
  C1 = Electrolytic Capacitor [capacitance=4.7µF voltage=16V package="100 mil [THT, electrolytic]"]
  4x1_5V = 4 x AAA Battery Mount

nets:
  GND: S1.Pin_1, S1.Pin_2, U1.GND, SPKR1.pin1, 4x1_5V.-
  N1: S1.Pin_3, S1.Pin_4, U1.D2
  N2: U1.D11_PWM/MOSI, C1.+
  N3: U1.VIN, 4x1_5V.+
  N4: SPKR1.pin2, C1.-
