# Fritzing sketch id2693_WT2003M03_Key_Control_Mode_0 (saved by Fritzing 0.8.5b)
breadboards: 1

parts:
  SPKR1 = Loudspeaker
  X1 = USB Connectors [package=usb-minib-nostop]
  K1_Play/Pause = Pushbutton [package="[THT]"]
  K2_Next = Pushbutton [package="[THT]"]
  K3_Previous = Pushbutton [package="[THT]"]
  WT2003M03-V1 = WT2003M03-V3

nets:
  N1: SPKR1.pin1, WT2003M03-V1.connector3
  N2: SPKR1.pin2, WT2003M03-V1.connector2
  N3: X1.GND, K1_Play/Pause.Pin_1, K1_Play/Pause.Pin_2, K1_Play/Pause.Pin_3, K1_Play/Pause.Pin_4, K2_Next.Pin_1, K2_Next.Pin_2, K2_Next.Pin_3, K2_Next.Pin_4, K3_Previous.Pin_1, K3_Previous.Pin_2, K3_Previous.Pin_3, K3_Previous.Pin_4, WT2003M03-V1.connector8, WT2003M03-V1.connector11, WT2003M03-V1.connector12
