# Fritzing sketch id2695_montage_imu_0 (saved by Fritzing 0.9.3b)

parts:
  Composant1 = Arduino Uno (Rev3)
  GY1 = MPU-6050 GY-521 [form="♀ (female)"]

nets:
  N1: Composant1.A4/SDA, GY1.connector3
  N2: Composant1.A5/SCL, GY1.connector2
  N3: Composant1.D2, GY1.connector7
  N4: Composant1.5V, GY1.connector0
  N5: Composant1.GND, GY1.connector1
