# Fritzing sketch id2697_montage_imu_servo_0 (saved by Fritzing 0.9.3b)

parts:
  Composant1 = Arduino Uno (Rev3)
  GY1 = MPU-6050 GY-521 [form="♀ (female)"]
  J1 = Basic Servo
  J2 = Basic Servo

nets:
  N1: Composant1.A4/SDA, GY1.connector3
  N2: Composant1.A5/SCL, GY1.connector2
  N3: Composant1.D9_PWM, J2.pulse
  N4: Composant1.D10_PWM/SS, J1.pulse
  N5: Composant1.D2, GY1.connector7
  5V: Composant1.5V, GY1.connector0, J2.vcc
  GND: Composant1.GND, GY1.connector1, J2.gnd
