# Fritzing sketch id2698_cir_0 (saved by Fritzing 0.9.3b)

parts:
  GY1 = MPU-6050 GY-521 [form="♀ (female)"]
  Part1 = Arduino Uno (Rev3) - ICSP

nets:
  N1: GY1.connector0, Part1.5V
  N2: GY1.connector1, Part1.GND
  N3: GY1.connector2, Part1.A5/SCL
  N4: GY1.connector3, Part1.A4/SDA
  N5: GY1.connector7, Part1.D2
