# Fritzing sketch id2699_MPU6050_02_0 (saved by Fritzing 0.9.2b)

parts:
  Parte2 = IMU Digital Combo Board 6DOF
  R1 = Resistor [tolerance=±5% resistance=220 package=THT]
  C1 = Ceramic Capacitor [capacitance=100nF package="100 mil [THT, multilayer]"]
  LED1 = LED - 5mm [color="Yellow (585nm)" package="5 mm [THT]"]
  Part4 = Arduino Pro Mini v13
  U1 = SD_CARD_SOCKET [package=sdcard_4uconn]
  C2 = Ceramic Capacitor [capacitance=100nF package="100 mil [THT, multilayer]"]
  SW1 = DIP SWITCH [package=dipswitch-02]
  SW2 = DIP SWITCH [package=dipswitch-02]
  Part5 = Arduino Pro Mini v13
  Part6 = FTDI Basic Programmer
  VCC1 = 4 x AAA Battery Mount
  JP1 = Header 3 [package=screwterminal-3.5mm-3_lock.007s]

nets:
  3.3V: Parte2.3.3V, C1.1, Part4.VCC, U1.CD_DAT3, SW1.1
  GND: Parte2.GND, C1.0, LED1.cathode, Part4.GND, U1.CLK, C2.0, SW2.2, VCC1.-, JP1.2
  N1: Parte2.SDA, Part4.A4
  N2: Parte2.SCL, Part4.A5
  N3: Parte2.INT0, Part4.D2
  N4: R1.Pin_0, Part4.D9_PWM
  N5: Part4.D13/SCK, U1.SH
  N6: Part4.D12/MISO, U1.CMD
  N7: Part4.D11_PWM/MOSI, U1.VSS1
  N8: Part4.D10_PWM/SS, U1.VDD
  N9: Part4.D5_PWM, SW1.3
  N10: Part4.D4, SW2.4
  N11: Part4.D3_PWM, SW2.3
  N12: C2.1, SW1.4, VCC1.+, JP1.3
  N13: Part5.DTR, Part6.DTR
  N14: Part5.D0/TX, Part6.RXI
  N15: Part5.D1/RX, Part6.TXO
  N16: Part5.VCC, Part6.POWER
  GND_2: Part5.GND, Part6.GND

notes:
  * GY521:
  INT -- D02
  SDA -- A04
  SCL -- A05
  * SD Card:
  MOSI -- D11
  MISO -- D12
  SCLK -- D13
  CS -- D10
  DIP 1-4 from left to right
