# Fritzing sketch id269_Ailgorbot_T.01_0 (saved by Fritzing 0.9.1b)
breadboards: 1

parts:
  Composant1 = IOIO for Android
  IC1 = L293D [package=THT]
  M2 = DC Motor
  J1 = Basic Servo
  J3 = Infrared Proximity Sensor
  M1 = DC Motor
  J2 = Basic Servo

nets:
  N1: Composant1.PIN7, IC1.In_1
  N2: Composant1.PIN8, IC1.In_2
  N3: Composant1.PIN11, IC1.In_4
  N4: Composant1.PIN12, IC1.In_3
  VCC: Composant1.VCC, IC1.+Vmotor, IC1.+V, J1.vcc, J3.Vcc, J2.vcc
  GND: Composant1.GND, IC1.0V, J1.gnd, J3.GND, J2.gnd
  N5: Composant1.PIN38, IC1.Enable_2
  N6: Composant1.PIN37, IC1.Enable_1
  N7: Composant1.PIN36, J2.pulse
  N8: Composant1.PIN35, J1.pulse
  N9: Composant1.PIN34, J3.Vout
  N10: IC1.Out_1_(_Controlled_by_Enable_1_), M1.pin_1
  N11: IC1.Out_2_(_Controlled_by_Enable_1_), M1.pin_2
  N12: IC1.Out_3_(_Controlled_by_Enable_2_), M2.pin_2
  N13: IC1.Out_4_(_Controlled_by_Enable_2_), M2.pin_1
