# Fritzing sketch id26_lauflicht_0 (saved by Fritzing 0.7.7b)
breadboards: 1

parts:
  R10 = Rotary Potentiometer (Small) [maximum_resistance=100kΩ]
  R11 = Resistor [tolerance=±5% resistance=680 package=THT]
  R12 = Resistor [tolerance=±5% resistance=680 package=THT]
  R13 = Resistor [tolerance=±5% resistance=680 package=THT]
  R14 = Resistor [tolerance=±5% resistance=680 package=THT]
  R15 = Resistor [tolerance=±5% resistance=680 package=THT]
  R16 = Resistor [tolerance=±5% resistance=680 package=THT]
  R17 = Resistor [tolerance=±5% resistance=680 package=THT]
  R18 = Resistor [tolerance=±5% resistance=680 package=THT]
  R19 = Resistor [tolerance=±5% resistance=680 package=THT]
  R20 = Resistor [tolerance=±5% resistance=680 package=THT]
  LED7 = LED - 5mm [color="Red (633nm)" package="5 mm [THT]"]
  LED16 = LED - 5mm [color="Red (633nm)" package="5 mm [THT]"]
  LED17 = LED - 5mm [color="Red (633nm)" package="5 mm [THT]"]
  LED18 = LED - 5mm [color="Red (633nm)" package="5 mm [THT]"]
  LED19 = LED - 5mm [color="Red (633nm)" package="5 mm [THT]"]
  LED20 = LED - 5mm [color="Red (633nm)" package="5 mm [THT]"]
  LED21 = LED - 5mm [color="Red (633nm)" package="5 mm [THT]"]
  LED22 = LED - 5mm [color="Red (633nm)" package="5 mm [THT]"]
  LED23 = LED - 5mm [color="Red (633nm)" package="5 mm [THT]"]
  LED24 = LED - 5mm [color="Red (633nm)" package="5 mm [THT]"]
  R21 = Resistor [tolerance=±5% resistance=10k package=THT]
  R22 = Resistor [tolerance=±5% resistance=10k package=THT]
  S3 = Pushbutton [package="[THT]"]
  S4 = Pushbutton [package="[THT]"]
  Arduino2 = Arduino

nets:
  N1: R10.leg1, R21.Pin_0, R22.Pin_0, Arduino2.+5V
  N2: R10.wiper, Arduino2.A0
  N3: R10.leg2, LED7.cathode, LED16.cathode, LED17.cathode, LED18.cathode, LED19.cathode, LED20.cathode, LED21.cathode, LED22.cathode, LED23.cathode, LED24.cathode, Arduino2.GND
  N4: R11.Pin_0, LED7.anode
  N5: R11.Pin_1, Arduino2.D13
  N6: R12.Pin_0, LED16.anode
  N7: R12.Pin_1, Arduino2.D12
  N8: R13.Pin_0, LED20.anode
  N9: R13.Pin_1, Arduino2.D7
  N10: R14.Pin_0, LED19.anode
  N11: R14.Pin_1, Arduino2.D6
  N12: R15.Pin_0, LED21.anode
  N13: R15.Pin_1, Arduino2.D8
  N14: R16.Pin_0, LED22.anode
  N15: R16.Pin_1, Arduino2.D9
  N16: R17.Pin_0, LED17.anode
  N17: R17.Pin_1, Arduino2.D4
  N18: R18.Pin_0, LED23.anode
  N19: R18.Pin_1, Arduino2.D10
  N20: R19.Pin_0, LED24.anode
  N21: R19.Pin_1, Arduino2.D11
  N22: R20.Pin_0, LED18.anode
  N23: R20.Pin_1, Arduino2.D5
  N24: R21.Pin_1, S4.Pin_3, S4.Pin_4, Arduino2.D2
  N25: R22.Pin_1, S3.Pin_3, S3.Pin_4, Arduino2.D3
  N26: S3.Pin_1, S3.Pin_2, S4.Pin_1, S4.Pin_2
