# Fritzing sketch id2700_Scheme_0 (saved by Fritzing 0.9.3b)
breadboards: 1

parts:
  На_голове = Arduino Nano (Rev3.0)
  К_MatLab = Arduino Uno (Rev3)
  Slave = Bluetooth HC-05 Macho
  GY1 = MPU-6050 GY-521 [form="♀ (female)"]
  Master = Bluetooth HC-05 Macho
  U1 = LIPO-1000mAh [package=lipo-1000]
  LED1 = LED - 5mm [color="Red (633nm)" package="5 mm [THT]"]

nets:
  N1: На_голове.D1/TX, Slave.RXD
  N2: На_голове.D0/RX, На_голове.RESET, Slave.TXD
  N3: На_голове.D2, GY1.connector7
  N4: На_голове.D12/MISO, LED1.anode
  GND: На_голове.GND, Slave.GND, GY1.connector1, U1.-, LED1.cathode
  5V: На_голове.5V, Slave.VCC, GY1.connector0, U1.+
  N5: На_голове.A5, GY1.connector2
  N6: На_голове.A4, GY1.connector3
  N7: К_MatLab.D0/RX, Master.TXD
  N8: К_MatLab.D1/TX, Master.RXD
  5V_2: К_MatLab.5V, Master.VCC
  GND_2: К_MatLab.GND, Master.GND

notes:
  Питается от батареи?
  Питается от USB
  Подает информацию в MatLab
