# Fritzing sketch id2701_MPX2010_Apm_interface_0 (saved by Fritzing 0.7.12b)
breadboards: 1

parts:
  U1 = LM124-324 Quad Opamp [package="DIP (Dual Inline)"]
  MPX1 = MPX2010 pressure sensor [part_number=MPX]
  R3 = Resistor [tolerance=±5% resistance=100k package=THT]
  R4 = Resistor [tolerance=±5% resistance=100k package=THT]
  R5 = Resistor [tolerance=±5% resistance=100k package=THT]
  R6 = Resistor [tolerance=±5% resistance=100k package=THT]
  R7 = Resistor [tolerance=±5% resistance=100k package=THT]
  R8 = Resistor [tolerance=±5% resistance=100k package=THT]
  J2 = Screw terminal - 2 pins [package=THT]
  J3 = Screw terminal - 2 pins [package=THT]
  R9 = Rotary Potentiometer (Small) [maximum_resistance=0.1MΩ]

nets:
  N1: U1.1OUT, U1.1IN-, J3.pin2
  N2: U1.1IN+, U1.2OUT, R7.Pin_1
  N3: U1.VCC+, MPX1.Vs, J2.pin2
  N4: U1.2IN+, R5.Pin_1, R7.Pin_0
  N5: U1.2IN-, R6.Pin_1, R8.Pin_0
  N6: U1.3OUT, R4.Pin_1, R5.Pin_0
  N7: U1.3IN-, R4.Pin_0, R9.wiper, R9.leg2
  N8: U1.3IN+, MPX1.V_out_+
  N9: U1.VCC-, MPX1.GND, R8.Pin_1, J2.pin1, J3.pin1
  N10: U1.4IN+, MPX1.V_out_-
  N11: U1.4IN-, R3.Pin_0, R9.leg1
  N12: U1.4OUT, R3.Pin_1, R6.Pin_0
