# Fritzing sketch id2702_Sketch_MQTT_node_4_buttons_4_leds_V0001_0 (saved by Fritzing 0.9.3b)
circuit board: 8.46667cm x 5.64444cm
breadboards: 1

parts:
  Part1 = Arduino Uno (Rev3)
  R1 = Resistor [tolerance=±5% resistance=220 package=THT]
  S1 = Pushbutton [package="[THT]"]
  S2 = Pushbutton [package="[THT]"]
  R2 = Resistor [tolerance=±5% resistance=220 package=THT]
  S3 = Pushbutton [package="[THT]"]
  S4 = Pushbutton [package="[THT]"]
  R3 = Resistor [tolerance=±5% resistance=220 package=THT]
  R4 = Resistor [tolerance=±5% resistance=220 package=THT]
  LED1 = LED - 5mm [color="Red (633nm)" package="5 mm [THT]"]
  LED2 = LED - 5mm [color="Red (633nm)" package="5 mm [THT]"]
  LED3 = LED - 5mm [color="Red (633nm)" package="5 mm [THT]"]
  LED4 = LED - 5mm [color="Red (633nm)" package="5 mm [THT]"]

nets:
  N1: Part1.D8, S2.Pin_1, S2.Pin_2
  N2: Part1.D10_PWM/SS, S1.Pin_1, S1.Pin_2
  N3: Part1.GND, S1.Pin_3, S1.Pin_4, S2.Pin_3, S2.Pin_4, S3.Pin_3, S3.Pin_4, S4.Pin_3, S4.Pin_4, LED1.cathode, LED2.cathode, LED3.cathode, LED4.cathode
  N4: Part1.D1/TX, R4.Pin_1
  N5: Part1.D2, R3.Pin_1
  N6: Part1.D3_PWM, R2.Pin_1
  N7: Part1.D5_PWM, R1.Pin_1
  N8: Part1.D6_PWM, S4.Pin_1, S4.Pin_2
  N9: Part1.D7, S3.Pin_1, S3.Pin_2
  N10: R1.Pin_0, LED1.anode
  N11: R2.Pin_0, LED2.anode
  N12: R3.Pin_0, LED3.anode
  N13: R4.Pin_0, LED4.anode

notes:
  MQTT-Ethernet-Node-4-buttons-4-leds
