# Fritzing sketch id2704_msgeq7_chip_breadboard_0 (saved by Fritzing 0.9.1b)
breadboards: 2

parts:
  MSGEQ1 = MSGEQ7_DIP
  C1 = Ceramic Capacitor [capacitance=0.1mF part_number=104 package="100 mil [THT, multilayer]"]
  Part1 = Arduino Uno (Rev3)
  C2 = Ceramic Capacitor [capacitance=10nF part_number=103 package="100 mil [THT, multilayer]"]
  R1 = Resistor [tolerance=±5% resistance=22k package=THT]
  TRS1 = Audio Jack (TRS) 3.5mm [package="4Ucon 08780 [THT]"]
  TRS2 = Audio Jack (TRS) 3.5mm [package="4Ucon 08780 [THT]"]
  R2 = Resistor [tolerance=±5% resistance=22k package=THT]
  C3 = Ceramic Capacitor [capacitance=0.1nF part_number=104 package="100 mil [THT, multilayer]"]
  R3 = Resistor [tolerance=±5% resistance=220k part_number=200k package=THT]
  C4 = Ceramic Capacitor [capacitance=100nF part_number=33 package="100 mil [THT, multilayer]"]
  TRS3 = Audio Jack (TRS) 3.5mm [package="4Ucon 08780 [THT]"]
  TRS4 = Audio Jack (TRS) 3.5mm [package="4Ucon 08780 [THT]"]
  MSGEQ2 = MSGEQ7_DIP
  R4 = Resistor [tolerance=±5% resistance=22k package=THT]
  C5 = Ceramic Capacitor [capacitance=10nF part_number=103 package="100 mil [THT, multilayer]"]
  R5 = Resistor [tolerance=±5% resistance=22k package=THT]
  C6 = Ceramic Capacitor [capacitance=100nF package="100 mil [THT, multilayer]"]
  C7 = Ceramic Capacitor [capacitance=100nF part_number=33 package="100 mil [THT, multilayer]"]
  C8 = Ceramic Capacitor [capacitance=0.1mF part_number=104 package="100 mil [THT, multilayer]"]

nets:
  N1: MSGEQ1.connector4, C2.0
  N2: MSGEQ1.connector5, C3.1
  N3: MSGEQ1.connector6, Part1.D13/SCK
  N4: MSGEQ1.connector7, R3.Pin_0, C4.1
  N5: C1.0, Part1.5V, R3.Pin_1
  N6: C1.1, Part1.GND, R2.Pin_1, C3.0, C4.0
  N7: C2.1, R1.Pin_0
  N8: R1.Pin_1, TRS1.Ring, TRS2.Ring, TRS2.Tip
  N9: TRS1.Sleeve, TRS2.Sleeve, R2.Pin_0
  N10: TRS3.Sleeve, TRS4.Sleeve, R4.Pin_0
  N11: TRS3.Ring, TRS3.Tip, TRS4.Ring, TRS4.Tip, R5.Pin_1
  N12: MSGEQ2.connector0, C7.1
  N13: MSGEQ2.connector2, C6.0
  N14: MSGEQ2.connector3, C5.0
  N15: MSGEQ2.connector6, R4.Pin_1, C6.1, C7.0, C8.1
  N16: MSGEQ2.connector7, C8.0
  N17: C5.1, R5.Pin_0
