# Fritzing sketch id2705_msgeq7_vis_0 (saved by Fritzing 0.9.3b)
breadboards: 1

parts:
  Part1 = Arduino Uno (Rev3)
  IC1 = MSGEQ7 [package=soic8]
  R1 = Resistor [tolerance=±5% resistance=220k package="2010 [SMD]"]
  C3 = Ceramic Capacitor [capacitance=0.1µF package="100 mil [THT, multilayer]"]
  C4 = Ceramic Capacitor [capacitance=0.1µF package="100 mil [THT, multilayer]"]
  TRS2 = Stereo Jack (TRS) 3.5mm [package="PG203J [THT]"]
  R2 = Resistor [tolerance=±5% resistance=22k package=THT]
  R3 = Resistor [tolerance=±5% resistance=22k package=THT]
  C5 = Ceramic Capacitor [capacitance=0.1µF package="100 mil [THT, multilayer]"]
  C8 = Ceramic Capacitor [capacitance=32pF package="100 mil [THT, multilayer]"]
  Part2 = ws2812b [package="smd 2812b"]
  R4 = Resistor [tolerance=±5% resistance=560 package=THT]

nets:
  N1: Part1.A0, IC1.DCOUT
  N2: Part1.D8, R4.Pin_0
  N3: Part1.D2, IC1.STROBE
  N4: Part1.D3_PWM, IC1.RESET
  GND: Part1.GND, IC1.GND, C3.1, TRS2.Sleeve, C5.1, C8.0, Part2.VSS
  VDD: Part1.VIN, IC1.VDD, R1.Pin_0, C5.0, Part2.VDD
  N5: IC1.AUDIO_IN, C4.0
  N6: IC1.CG, C3.0
  N7: IC1.CKIN, R1.Pin_1, C8.1
  N8: C4.1, R2.Pin_1, R3.Pin_1
  N9: TRS2.Ring, R3.Pin_0
  N10: TRS2.Tip, R2.Pin_0
  N11: Part2.DIN, R4.Pin_1
