# Fritzing sketch id2706_msp430_msgeq7_0 (saved by Fritzing 0.7.10b)
stripboards: 2

parts:
  a0 = female pin header, 12 pins [form="♀ (female)"]
  a1 = female pin header, 12 pins [form="♀ (female)"]
  a2 = female pin header, 12 pins [form="♀ (female)"]
  a3 = female pin header, 12 pins [form="♀ (female)"]
  a4 = female pin header, 12 pins [form="♀ (female)"]
  a5 = female pin header, 12 pins [form="♀ (female)"]
  a6 = female pin header, 12 pins [form="♀ (female)"]
  a7 = female pin header, 12 pins [form="♀ (female)"]
  a8 = female pin header, 12 pins [form="♀ (female)"]
  a9 = female pin header, 12 pins [form="♀ (female)"]
  a10 = female pin header, 12 pins [form="♀ (female)"]
  a11 = female pin header, 12 pins [form="♀ (female)"]
  a12 = female pin header, 12 pins [form="♀ (female)"]
  a13 = female pin header, 12 pins [form="♀ (female)"]
  a14 = female pin header, 12 pins [form="♀ (female)"]
  a15 = female pin header, 12 pins [form="♀ (female)"]
  MSP430 = IC, DIP package, 20 pins [chip_label=IC]
  Rst = female pin header, 2 pins [form="♀ (female)"]
  MSGEQ7 = IC, DIP package, 8 pins [chip_label=IC]
  GND = female pin header, 3 pins [form="♀ (female)"]
  GND_2 = female pin header, 3 pins [form="♀ (female)"]
  J5 = female pin header, 1 pin [form="♀ (female)"]
  J6 = female pin header, 1 pin [form="♀ (female)"]
  J7 = female pin header, 1 pin [form="♀ (female)"]
  J8 = female pin header, 1 pin [form="♀ (female)"]
  J9 = female pin header, 1 pin [form="♀ (female)"]
  R1 = Resistor [tolerance=±5% resistance=22k package=THT]
  R2 = Resistor [tolerance=±5% resistance=22k package=THT]
  62870 = Ceramic Capacitor [capacitance=10pF package="100 mil [THT, multilayer]"]
  C3 = Ceramic Capacitor [capacitance=100nF package="100 mil [THT, multilayer]"]
  R6 = Resistor [tolerance=±5% resistance=330k package=THT]
  R7 = Resistor [tolerance=±5% resistance=470k package=THT]
  www_simpleavr_com = Resistor [tolerance=±5% resistance=220k package=THT]
  C1 = Ceramic Capacitor [capacitance=10nF package="100 mil [THT, multilayer]"]
  C4 = Ceramic Capacitor [capacitance=100nF package="100 mil [THT, multilayer]"]
  R9 = Resistor [tolerance=±5% resistance=470k package=THT]

nets:
  N1: a0.pin1, a0.pin7, a2.pin1, a2.pin7, a4.pin1, a4.pin7, a6.pin1, a6.pin7, a8.pin1, a8.pin7, a10.pin1, a10.pin7, a12.pin1, a12.pin7, a14.pin1, a14.pin7, MSP430.pin16
  N2: a0.pin2, a0.pin8, a2.pin2, a2.pin8, a4.pin2, a4.pin8, a6.pin2, a6.pin8, a8.pin2, a8.pin8, a10.pin2, a10.pin8, a12.pin2, a12.pin8, a14.pin2, a14.pin8, MSP430.pin15
  N3: a0.pin3, a0.pin9, a2.pin3, a2.pin9, a4.pin3, a4.pin9, a6.pin3, a6.pin9, a8.pin3, a8.pin9, a10.pin3, a10.pin9, a12.pin3, a12.pin9, a14.pin3, a14.pin9, MSP430.pin14
  N4: a0.pin4, a0.pin10, a2.pin4, a2.pin10, a4.pin4, a4.pin10, a6.pin4, a6.pin10, a8.pin4, a8.pin10, a10.pin4, a10.pin10, a12.pin4, a12.pin10, a14.pin4, a14.pin10, MSP430.pin13
  N5: a0.pin5, a0.pin11, a2.pin5, a2.pin11, a4.pin5, a4.pin11, a6.pin5, a6.pin11, a8.pin5, a8.pin11, a10.pin5, a10.pin11, a12.pin5, a12.pin11, a14.pin5, a14.pin11, MSP430.pin12
  N6: a0.pin6, a0.pin12, a2.pin6, a2.pin12, a4.pin6, a4.pin12, a6.pin6, a6.pin12, a8.pin6, a8.pin12, a10.pin6, a10.pin12, a12.pin6, a12.pin12, a14.pin6, a14.pin12, MSP430.pin11
  N7: a1.pin1, a1.pin2, a1.pin3, a1.pin4, a1.pin5, a1.pin6, a1.pin7, a1.pin8, a1.pin9, a1.pin10, a1.pin11, a1.pin12, MSP430.pin10
  N8: a3.pin1, a3.pin2, a3.pin3, a3.pin4, a3.pin5, a3.pin6, a3.pin7, a3.pin8, a3.pin9, a3.pin10, a3.pin11, a3.pin12, MSP430.pin9
  N9: a5.pin1, a5.pin2, a5.pin3, a5.pin4, a5.pin5, a5.pin6, a5.pin7, a5.pin8, a5.pin9, a5.pin10, a5.pin11, a5.pin12, MSP430.pin8
  N10: a7.pin1, a7.pin2, a7.pin3, a7.pin4, a7.pin5, a7.pin6, a7.pin7, a7.pin8, a7.pin9, a7.pin10, a7.pin11, a7.pin12, MSP430.pin7
  N11: a9.pin1, a9.pin2, a9.pin3, a9.pin4, a9.pin5, a9.pin6, a9.pin7, a9.pin8, a9.pin9, a9.pin10, a9.pin11, a9.pin12, MSP430.pin6
  N12: a11.pin1, a11.pin2, a11.pin3, a11.pin4, a11.pin5, a11.pin6, a11.pin7, a11.pin8, a11.pin9, a11.pin10, a11.pin11, a11.pin12, MSP430.pin3, R7.Pin_1
  N13: a13.pin1, a13.pin2, a13.pin3, a13.pin4, a13.pin5, a13.pin6, a13.pin7, a13.pin8, a13.pin9, a13.pin10, a13.pin11, a13.pin12, MSP430.pin2, R6.Pin_1
  N14: a15.pin1, a15.pin2, a15.pin3, a15.pin4, a15.pin5, a15.pin6, a15.pin7, a15.pin8, a15.pin9, a15.pin10, a15.pin11, a15.pin12, MSP430.pin17, MSGEQ7.pin4
  N15: MSP430.pin1, MSGEQ7.pin2, GND.pin1, GND_2.pin1, J7.pin1, J9.pin1, 62870.1, C3.0, C4.1
  N16: MSP430.pin4, Rst.pin2
  N17: MSP430.pin5, Rst.pin1, R9.Pin_1
  N18: MSP430.pin18, MSGEQ7.pin7, GND.pin3, GND_2.pin3
  N19: MSP430.pin19, MSGEQ7.pin3
  N20: MSP430.pin20, MSGEQ7.pin1, GND.pin2, GND_2.pin2, www_simpleavr_com.Pin_0, C4.0, R9.Pin_0
  N21: MSGEQ7.pin5, C1.1
  N22: MSGEQ7.pin6, C3.1
  N23: MSGEQ7.pin8, 62870.0, R6.Pin_0, R7.Pin_0, www_simpleavr_com.Pin_1
  N24: J5.pin1, J8.pin1, R2.Pin_1
  N25: J6.pin1, R1.Pin_1
  N26: R1.Pin_0, R2.Pin_0, C1.0
