# Fritzing sketch id2707_Gregor_Bruhin___Multi_Alarm_Fire_Temperature_Humidity_Sensor_Shield_0 (saved by Fritzing 0.7.4b)
breadboards: 1

parts:
  R2 = Resistor [tolerance=±5% resistance=10k package=THT]
  R3 = Resistor [tolerance=±5% resistance=10k package=THT]
  R4 = Resistor [tolerance=±5% resistance=10k package=THT]
  R5 = Resistor [tolerance=±5% resistance=10k package=THT]
  5v_Signal = screw terminal, 6 pins
  Input = screw terminal, 6 pins
  Sensor_Shield = Arduino Ethernet Shield
  R6 = Resistor [tolerance=±5% resistance=10k package=THT]
  LED1 = LED - 5mm [color="Green (555nm)" package="5 mm [THT]"]
  LED2 = LED - 5mm [color="Red (633nm)" package="5 mm [THT]"]
  u2 = mystery part, 8 pins [chip_label=U2 spacing=300mil]
  U1 = mystery part, 2 pins [chip_label=? spacing=300mil]
  R7 = Resistor [tolerance=±5% resistance=220 package=THT]
  R9 = Resistor [tolerance=±5% resistance=220 package=THT]
  DHT = Humidity and Temperature Sensor RHT03
  R1 = Resistor [tolerance=±5% resistance=10k package=THT]

nets:
  N1: R2.Pin_0, R3.Pin_0, R4.Pin_0, R5.Pin_0, Sensor_Shield.GND, R6.Pin_0, LED1.cathode, LED2.cathode, DHT.GND_1, DHT.GND_2, R1.Pin_0
  N2: R2.Pin_1, Input.pin5, Sensor_Shield.A1
  N3: R3.Pin_1, Input.pin4, Sensor_Shield.A2
  N4: R4.Pin_1, Input.pin3, Sensor_Shield.A3
  N5: R5.Pin_1, Input.pin2, Sensor_Shield.A4
  +5V: 5v_Signal.pin1, 5v_Signal.pin2, 5v_Signal.pin3, 5v_Signal.pin4, 5v_Signal.pin5, 5v_Signal.pin6, Sensor_Shield.+5V, DHT.Vcc
  N6: Input.pin1, Sensor_Shield.A5, R6.Pin_1
  N7: Input.pin6, Sensor_Shield.A0, R1.Pin_1
  N8: Sensor_Shield.D9, U1.pin2, R7.Pin_0
  N9: Sensor_Shield.D8, U1.pin1, R9.Pin_0
  N10: Sensor_Shield.D7, u2.pin8, DHT.Data-signal
  N11: Sensor_Shield.D6, u2.pin7
  N12: Sensor_Shield.D5, u2.pin6
  N13: Sensor_Shield.D3, u2.pin4
  N14: Sensor_Shield.D2, u2.pin3
  N15: Sensor_Shield.D1TX, u2.pin2
  N16: Sensor_Shield.D0RX, u2.pin1
  N17: LED1.anode, R7.Pin_1
  N18: LED2.anode, R9.Pin_1

notes:
  A0
  A1
  A2
  A4
  A5
  A3
