# Fritzing sketch id270_Ailgorbot_T.02_0 (saved by Fritzing 0.9.1b)
breadboards: 1

parts:
  IC1 = L293D [package=THT]
  M2 = DC Motor
  J1 = Basic Servo
  J3 = Infrared Proximity Sensor
  M1 = DC Motor
  J2 = Basic Servo
  U1 = LIPO-2000mAh [package=lipo-2000]
  Composant1 = IOIO for Android

nets:
  N1: IC1.Enable_1, Composant1.PIN37
  N2: IC1.In_1, Composant1.PIN7
  N3: IC1.Out_1_(_Controlled_by_Enable_1_), M1.pin_1
  GND: IC1.0V, J1.gnd, J3.GND, J2.gnd, U1.-, Composant1.GND
  N4: IC1.Out_2_(_Controlled_by_Enable_1_), M1.pin_2
  N5: IC1.In_2, Composant1.PIN8
  VCC: IC1.+Vmotor, IC1.+V, J1.vcc, J3.Vcc, J2.vcc, Composant1.5V
  N6: IC1.Enable_2, Composant1.PIN38
  N7: IC1.In_3, Composant1.PIN12
  N8: IC1.Out_3_(_Controlled_by_Enable_2_), M2.pin_2
  N9: IC1.Out_4_(_Controlled_by_Enable_2_), M2.pin_1
  N10: IC1.In_4, Composant1.PIN11
  N11: J1.pulse, Composant1.PIN35
  N12: J3.Vout, Composant1.PIN34
  N13: J2.pulse, Composant1.PIN36
  N14: U1.+, Composant1.VCC
