# Fritzing sketch id2710_omk_mtr_24_1_0 (saved by Fritzing 0.7.4b)
breadboards: 1

parts:
  Maple_Mini = IC, DIP package, 40 pins [chip_label="Maple Mini" spacing=600mil]
  MUXA = IC, DIP package, 16 pins [chip_label=74HC4052 spacing=300mil]
  A1 = A1301
  part = female pin header, 6 pins [form="♀ (female)"]
  WIZ820io = female pin header, 6 pins [form="♀ (female)"]
  A2 = A1301
  A3 = A1301
  A4 = A1301
  A5 = A1301
  A6 = A1301
  A7 = A1301
  A8 = A1301
  B1 = A1301
  B2 = A1301
  B3 = A1301
  B4 = A1301
  B5 = A1301
  B6 = A1301
  B7 = A1301
  B8 = A1301
  C1 = A1301
  C2 = A1301
  C3 = A1301
  C4 = A1301
  C5 = A1301
  C6 = A1301
  C7 = A1301
  C8 = A1301
  MUXB = IC, DIP package, 16 pins [chip_label=74HC4052 spacing=300mil]
  MUXC = IC, DIP package, 16 pins [chip_label=74HC4052 spacing=300mil]

nets:
  N1: Maple_Mini.pin5, MUXA.pin13
  N2: Maple_Mini.pin6, MUXC.pin3
  N3: Maple_Mini.pin7, MUXB.pin13
  N4: Maple_Mini.pin8, MUXB.pin3
  N5: Maple_Mini.pin9, MUXC.pin13
  N6: Maple_Mini.pin10, MUXA.pin3
  N7: Maple_Mini.pin11, MUXA.pin10, MUXB.pin10, MUXC.pin10
  N8: Maple_Mini.pin12, MUXA.pin9, MUXB.pin9, MUXC.pin9
  N9: Maple_Mini.pin14, part.pin5
  N10: Maple_Mini.pin15, part.pin4
  N11: Maple_Mini.pin19, MUXA.pin6, MUXA.pin7, MUXA.pin8, A1.connector1, A2.connector1, A3.connector1, A4.connector1, A5.connector1, A6.connector1, A7.connector1, A8.connector1, B1.connector1, B2.connector1, B3.connector1, B4.connector1, B5.connector1, B6.connector1, B7.connector1, B8.connector1, C1.connector1, C2.connector1, C3.connector1, C4.connector1, C5.connector1, C6.connector1, C7.connector1, C8.connector1, MUXB.pin6, MUXB.pin7, MUXB.pin8, MUXC.pin6, MUXC.pin7, MUXC.pin8
  N12: Maple_Mini.pin20, MUXA.pin16, A1.connector0, A2.connector0, A3.connector0, A4.connector0, A5.connector0, A6.connector0, A7.connector0, A8.connector0, B1.connector0, B2.connector0, B3.connector0, B4.connector0, B5.connector0, B6.connector0, B7.connector0, B8.connector0, C1.connector0, C2.connector0, C3.connector0, C4.connector0, C5.connector0, C6.connector0, C7.connector0, C8.connector0, MUXB.pin16, MUXC.pin16
  N13: Maple_Mini.pin21, part.pin2, part.pin3
  N14: Maple_Mini.pin22, part.pin1, WIZ820io.pin1, WIZ820io.pin2
  N15: Maple_Mini.pin28, WIZ820io.pin6
  N16: Maple_Mini.pin37, WIZ820io.pin3
  N17: Maple_Mini.pin38, part.pin6
  N18: Maple_Mini.pin39, WIZ820io.pin4
  N19: Maple_Mini.pin40, WIZ820io.pin5
  N20: MUXA.pin1, A3.connector2
  N21: MUXA.pin2, A4.connector2
  N22: MUXA.pin4, A5.connector2
  N23: MUXA.pin5, A6.connector2
  N24: MUXA.pin11, A8.connector2
  N25: MUXA.pin12, A7.connector2
  N26: MUXA.pin14, A2.connector2
  N27: MUXA.pin15, A1.connector2
  N28: B1.connector2, MUXB.pin15
  N29: B2.connector2, MUXB.pin14
  N30: B3.connector2, MUXB.pin1
  N31: B4.connector2, MUXB.pin2
  N32: B5.connector2, MUXB.pin4
  N33: B6.connector2, MUXB.pin5
  N34: B7.connector2, MUXB.pin12
  N35: B8.connector2, MUXB.pin11
  N36: C1.connector2, MUXC.pin15
  N37: C2.connector2, MUXC.pin14
  N38: C3.connector2, MUXC.pin1
  N39: C4.connector2, MUXC.pin2
  N40: C5.connector2, MUXC.pin4
  N41: C6.connector2, MUXC.pin5
  N42: C7.connector2, MUXC.pin12
  N43: C8.connector2, MUXC.pin11
