# Fritzing sketch id2711_multicolorLED_NLCCLab_ArduinoHomework_0 (saved by Fritzing 0.8.3b)
breadboards: 1

parts:
  LED1 = RGB LED (com. anode, rbg) [package="5 mm [THT]"]
  R1 = Resistor [tolerance=±5% resistance=220 package=THT]
  R2 = Resistor [tolerance=±5% resistance=220 package=THT]
  R3 = Resistor [tolerance=±5% resistance=220 package=THT]
  S1 = Pushbutton [package="[THT]"]
  R4 = Trimmer Potentiometer [maximum_resistance=10kΩ package=THT]
  Part1 = Arduino Uno (Rev3)
  R5 = Resistor [tolerance=±20% resistance=10k package=THT]

nets:
  N1: LED1.red_cathode, R1.Pin_0
  N2: LED1.common_anode, R4.leg2, Part1.GND, R5.Pin_0
  N3: LED1.blue_cathode, R2.Pin_0
  N4: LED1.green_cathode, R3.Pin_0
  N5: R1.Pin_1, S1.Pin_3, S1.Pin_4, Part1.D2, R5.Pin_1
  N6: R2.Pin_1, R4.wiper, Part1.A0
  N7: R3.Pin_1, Part1.ICSP_MOSI, Part1.D11_PWM/MOSI
  N8: S1.Pin_1, S1.Pin_2, R4.leg1, Part1.5V
