# Fritzing sketch id2712_LED19_0 (saved by Fritzing 0.3.12b)
breadboards: 1

parts:
  Arduino1 = Arduino
  RGB1 = screw terminal, 4 pins
  ULN2003 = IC, DIP package, 16 pins [chip_label=IC spacing=300mil]
  RGB2 = screw terminal, 4 pins
  PWR = female pin header, 2 pins [form="♂ (male)"]
  RESET = Pushbutton [package="[THT]"]
  S1 = Pushbutton [package="[THT]"]
  VREG = Voltage Regulator - 5V [package="TO220 [THT]"]
  C1 = Electrolytic Capacitor [package=THT]
  S1_2 = Toggle Switch [package=THT]
  Power_plug1 = Power plug
  LED1 = Red LED - 5mm
  R1 = Resistor [resistance=220 package=THT]
  C2 = Electrolytic Capacitor [package=THT]
  R2 = Trimmer Potentiometer [package=THT]

nets:
  GND: Arduino1.GND, ULN2003.pin8, RESET.Pin_3, RESET.Pin_4, S1.Pin_3, S1.Pin_4, VREG.GND, C1.-, S1_2.L2, Power_plug1.GND, LED1.cathode, C2.-, R2.leg2
  N1: Arduino1.D13, R1.Pin_1
  N2: Arduino1.D12, S1.Pin_1, S1.Pin_2
  N3: Arduino1.D11, ULN2003.pin6
  N4: Arduino1.D10, ULN2003.pin5
  N5: Arduino1.D9, ULN2003.pin4
  N6: Arduino1.D6, ULN2003.pin3
  N7: Arduino1.D5, ULN2003.pin2
  N8: Arduino1.D3, ULN2003.pin1
  N9: Arduino1.RST, RESET.Pin_1, RESET.Pin_2
  N10: Arduino1.+5V, R2.leg1
  N11: Arduino1.VIN, PWR.pin2
  N12: Arduino1.A0, R2.wiper
  N13: RGB1.pin1, ULN2003.pin9, RGB2.pin1, PWR.pin1, VREG.output_voltage, C2.+
  N14: RGB1.pin2, ULN2003.pin16
  N15: RGB1.pin3, ULN2003.pin15
  N16: RGB1.pin4, ULN2003.pin14
  N17: ULN2003.pin11, RGB2.pin4
  N18: ULN2003.pin12, RGB2.pin3
  N19: ULN2003.pin13, RGB2.pin2
  N20: VREG.input_voltage, C1.+, S1_2.COM
  N21: S1_2.L1, Power_plug1.VCC
  N22: LED1.anode, R1.Pin_0

notes:
  Multicolor RGB LED Controller Shield
  by Szymon Kobalczyk
  Connect external DC power supply
  12V voltage regulator
  Jumper to select internal or external power
  (dont' use both!)
  Terminals for RGB LED strips
  12V voltage
  regulator
  External DC power supply
  Potentiometer and button to select color modes
  Jumper to select internal or external power
  (Dont' use both!)
  ULN2003 IC
