# Fritzing sketch id2713_Mybuttons_0 (saved by Fritzing 0.7.12b)
breadboards: 1

parts:
  S1 = Pushbutton [package="[THT]"]
  R1 = Resistor [tolerance=±5% resistance=10 package=THT]
  S2 = Pushbutton [package="[THT]"]
  R2 = Resistor [tolerance=±5% resistance=10 package=THT]
  S3 = Pushbutton [package="[THT]"]
  S4 = Pushbutton [package="[THT]"]
  S5 = Pushbutton [package="[THT]"]
  R3 = Resistor [tolerance=±5% resistance=10 package=THT]
  R4 = Resistor [tolerance=±5% resistance=10 package=THT]
  R5 = Resistor [tolerance=±5% resistance=10 package=THT]
  Arduino1 = Arduino
  LED1 = LED - 5mm [color="Red (633nm)" package="5 mm [THT]"]
  LED2 = LED - 5mm [color="Green (560nm)" package="5 mm [THT]"]

nets:
  N1: S1.Pin_1, S1.Pin_2, R1.Pin_0, Arduino1.D0RX
  N2: S1.Pin_3, S1.Pin_4, S2.Pin_3, S2.Pin_4, S3.Pin_3, S3.Pin_4, S4.Pin_3, S4.Pin_4, S5.Pin_3, S5.Pin_4, Arduino1.+5V
  N3: R1.Pin_1, R2.Pin_1, R3.Pin_1, R4.Pin_1, R5.Pin_1, Arduino1.GND, Arduino1.D13, LED2.anode
  N4: S2.Pin_1, S2.Pin_2, R2.Pin_0, Arduino1.D1TX
  N5: S3.Pin_1, S3.Pin_2, R3.Pin_0, Arduino1.D2
  N6: S4.Pin_1, S4.Pin_2, R4.Pin_0, Arduino1.D3
  N7: S5.Pin_1, S5.Pin_2, R5.Pin_0, Arduino1.D4
  N8: Arduino1.D12, LED2.cathode
  N9: LED1.cathode, LED1.anode
