# Fritzing sketch id2714_FHA8FABGZMIUHMM (saved by Fritzing 0.6.3b)
breadboards: 1

parts:
  IC1 = IC, DIP package, 8 pins [chip_label=TL082 spacing=300mil]
  R1 = Resistor [tolerance=±5% resistance=1M package=THT]
  R2 = Resistor [tolerance=±5% resistance=510k package=THT]
  R3 = Resistor [tolerance=±5% resistance=330k package=THT]
  R4 = Resistor [tolerance=±5% resistance=4.7k package=THT]
  R5 = Resistor [tolerance=±5% resistance=12k package=THT]
  C1 = Ceramic Capacitor [capacitance=5pF voltage=16V package="100 mil [THT, multilayer]"]
  C2 = Ceramic Capacitor [capacitance=100nF voltage=16V package="100 mil [THT, multilayer]"]
  C3 = Electrolytic Capacitor [capacitance=1µF package="100 mil [THT, electrolytic]"]
  C4 = Ceramic Capacitor [capacitance=82nF voltage=16V package="100 mil [THT, multilayer]"]
  R6 = Resistor [tolerance=±5% resistance=1M package=THT]
  R7 = Resistor [tolerance=±5% resistance=10k package=THT]
  R8 = Resistor [tolerance=±5% resistance=10k package=THT]
  C5 = Electrolytic Capacitor [capacitance=1µF package="100 mil [THT, electrolytic]"]
  C6 = Electrolytic Capacitor [capacitance=1µF package="100 mil [THT, electrolytic]"]
  IC2 = Arduino
  9V1 = 9V Battery
  R9 = Rotary Potentiometer (Small) [maximum_resistance=100kΩ]
  R10 = Rotary Potentiometer (Small) [maximum_resistance=100kΩ]
  R11 = Resistor [tolerance=±5% resistance=1k package=THT]
  C7 = Electrolytic Capacitor [capacitance=1µF package="100 mil [THT, electrolytic]"]
  R12 = Resistor [tolerance=±5% resistance=10k package=THT]
  R13 = Resistor [tolerance=±5% resistance=1k package=THT]
  R14 = Resistor [tolerance=±5% resistance=220 package=THT]
  R15 = Resistor [tolerance=±5% resistance=1.5k package=THT]
  R16 = Resistor [tolerance=±5% resistance=390k package=THT]
  R17 = Rotary Potentiometer (Small) [maximum_resistance=100kΩ]
  Rotary_Switch = Jack_1_4
  C8 = Electrolytic Capacitor [capacitance=47µF voltage=50V package="100 mil [THT, electrolytic]"]
  R18 = Resistor [tolerance=±5% resistance=10k package=THT]
  R19 = Resistor [tolerance=±5% resistance=10k package=THT]
  C9 = Electrolytic Capacitor [capacitance=47µF voltage=50V package="100 mil [THT, electrolytic]"]
  R20 = Resistor [tolerance=±5% resistance=100k package=THT]
  R21 = Resistor [tolerance=±5% resistance=100k package=THT]
  R22 = Resistor [tolerance=±5% resistance=68k package=THT]
  R23 = Resistor [tolerance=±5% resistance=47k package=THT]
  R24 = Resistor [tolerance=±5% resistance=33k package=THT]
  R25 = Resistor [tolerance=±5% resistance=22k package=THT]
  R26 = Resistor [tolerance=±5% resistance=10k package=THT]
  DPDT_pushbutton_switch = DPDT_Pushbutton_Switch

nets:
  N1: IC1.pin1, R5.Pin_0, C2.0, C3.+
  N2: IC1.pin2, R5.Pin_1, C2.1, R7.Pin_1, R8.Pin_1
  N3: IC1.pin3, R4.Pin_0
  N4: IC1.pin4, R6.Pin_1, IC2.GND, 9V1.connector1, R9.leg1, R10.leg1, R14.Pin_0, R17.leg1, C8.-, R18.Pin_0, C9.-, R20.Pin_1
  N5: IC1.pin5, R3.Pin_0
  N6: IC1.pin6, R1.Pin_1, R2.Pin_0, C1.1
  N7: IC1.pin7, R1.Pin_0, C1.0, R9.leg2, R11.Pin_1
  N8: IC1.pin8, IC2.VIN, 9V1.connector0, C8.+, R19.Pin_0
  N9: R2.Pin_1, C4.0
  N10: R3.Pin_1, R4.Pin_1, R18.Pin_1, R19.Pin_1, C9.+
  N11: C3.-, DPDT_pushbutton_switch.connector4
  N12: C4.1, R6.Pin_0, DPDT_pushbutton_switch.connector5
  N13: R7.Pin_0, C5.+
  N14: R8.Pin_0, C6.-
  N15: C5.-, R10.wiper
  N16: C6.+, R9.wiper
  N17: IC2.aref, R17.leg2, R21.Pin_1, R22.Pin_1, R23.Pin_1, R24.Pin_1, R25.Pin_1, R26.Pin_1
  N18: IC2.D11, R16.Pin_0
  N19: IC2.D3, R15.Pin_0
  N20: IC2.+5V, R12.Pin_0
  N21: IC2.A0, C7.-, R12.Pin_1, R13.Pin_1
  N22: IC2.A2, Rotary_Switch.connector2, R20.Pin_0
  N23: IC2.A3, R17.wiper
  N24: R10.leg2, R15.Pin_1, R16.Pin_1
  N25: R11.Pin_0, C7.+
  N26: R13.Pin_0, R14.Pin_1
  N27: Rotary_Switch.connector4, R26.Pin_0
  N28: Rotary_Switch.connector6, R25.Pin_0
  N29: Rotary_Switch.connector7, R24.Pin_0
  N30: Rotary_Switch.connector10, R21.Pin_0
  N31: Rotary_Switch.connector11, R22.Pin_0
  N32: Rotary_Switch.connector12, R23.Pin_0
  N33: DPDT_pushbutton_switch.connector8, DPDT_pushbutton_switch.connector9
