# Fritzing sketch id2714_Untitled_Sketch_0 (saved by Fritzing 0.7.4b)
breadboards: 1

parts:
  Arduino1 = Arduino
  LED1 = LED - 5mm [color="Red (633nm)" package="5 mm [THT]"]
  LED2 = LED - 5mm [color="Red (633nm)" package="5 mm [THT]"]
  LED3 = LED - 5mm [color="Red (633nm)" package="5 mm [THT]"]
  LED4 = LED - 5mm [color="Red (633nm)" package="5 mm [THT]"]  # not connected
  LED5 = LED - 5mm [color="Red (633nm)" package="5 mm [THT]"]  # not connected

nets:
  N1: Arduino1.GND, LED1.anode, LED2.anode
  N2: Arduino1.D6, LED2.cathode
  N3: Arduino1.D5, LED3.cathode
  N4: Arduino1.D3, LED1.cathode

notes:
  + POSITIVE
  - NEGATIVE
