# Fritzing sketch id2715_project (saved by Fritzing 0.6.4b)
breadboards: 3

parts:
  Q1 = NPN-Transistor [package="TO92 [THT]"]
  R1 = Resistor [tolerance=±5% resistance=10k package=THT]
  VCC1 = 4 x AAA Battery Mount
  R2 = Resistor [tolerance=±5% resistance=10k package=THT]
  Q2 = NPN-Transistor [package="TO92 [THT]"]
  R3 = Resistor [tolerance=±5% resistance=10k package=THT]
  R4 = Resistor [tolerance=±5% resistance=10k package=THT]
  VCC2 = 4 x AAA Battery Mount
  Q3 = NPN-Transistor [package="TO92 [THT]"]
  R5 = Resistor [tolerance=±5% resistance=10k package=THT]
  Q4 = NPN-Transistor [package="TO92 [THT]"]
  R6 = Resistor [tolerance=±5% resistance=10k package=THT]
  VCC3 = 4 x AAA Battery Mount
  Q5 = NPN-Transistor [package="TO92 [THT]"]
  R7 = Resistor [tolerance=±5% resistance=10k package=THT]
  R9 = Resistor [tolerance=±5% resistance=10k package=THT]
  R10 = Resistor [tolerance=±5% resistance=10k package=THT]

nets:
  N1: Q1.E, R1.Pin_1
  N2: Q1.B, R2.Pin_0
  N3: Q1.C, R1.Pin_0, VCC1.+
  N4: Q2.E, R4.Pin_1
  N5: Q2.C, R3.Pin_0, Q3.C
  N6: R3.Pin_1, VCC2.-
  N7: R4.Pin_0, VCC2.+, R5.Pin_0
  N8: Q3.E, R5.Pin_1
  N9: Q4.E, R6.Pin_1
  N10: Q4.B, R10.Pin_0
  N11: Q4.C, Q5.E
  N12: R6.Pin_0, VCC3.+
  N13: VCC3.-, R9.Pin_1
  N14: Q5.B, R7.Pin_0
  N15: Q5.C, R9.Pin_0

notes:
  NOT GATE
  INPUT
  OUTPUT
  INPUT 1 and 2
  OR GATE
  AND GATE
