# Fritzing sketch id2717_Arduino_Charlieplexing_LEDs_on_a_breadboard_0 (saved by Fritzing 0.4.3b)
breadboards: 1

parts:
  LED1 = Red LED - 5mm
  LED1_2 = Blue LED - 5mm
  LED1_3 = Blue LED - 5mm
  LED1_4 = Red LED - 5mm
  LED1_5 = Blue LED - 5mm
  LED1_6 = Red LED - 5mm
  LED1_7 = green LED - 5mm
  LED1_8 = green LED - 5mm
  LED1_9 = green LED - 5mm
  Q1 = NPN-Transistor [package="TO92 [THT]"]
  Q2 = NPN-Transistor [package="TO92 [THT]"]
  Q3 = NPN-Transistor [package="TO92 [THT]"]
  R1 = Resistor [resistance=10k package=THT]
  R1_2 = Resistor [resistance=10k package=THT]
  R1_3 = Resistor [resistance=10k package=THT]
  R2 = Resistor [resistance=15k package=THT]
  R2_2 = Resistor [resistance=15k package=THT]
  R2_3 = Resistor [resistance=15k package=THT]
  Arduino1 = Arduino

nets:
  N1: LED1.cathode, LED1_5.cathode, LED1_9.cathode, R1_2.Pin_0
  N2: LED1.anode, LED1_3.anode, LED1_7.anode, Arduino1.D12
  N3: LED1_2.cathode, LED1_4.cathode, LED1_7.cathode, R1.Pin_0
  N4: LED1_2.anode, LED1_6.anode, LED1_9.anode, Arduino1.D11
  N5: LED1_3.cathode, LED1_6.cathode, LED1_8.anode, R1_3.Pin_0
  N6: LED1_4.anode, LED1_5.anode, LED1_8.cathode, Arduino1.D13
  N7: Q1.E, R1.Pin_1
  N8: Q1.B, R2.Pin_0
  N9: Q1.C, Q2.C, Q3.C
  N10: Q2.E, R1_2.Pin_1
  N11: Q2.B, R2_3.Pin_0
  N12: Q3.E, R1_3.Pin_1
  N13: Q3.B, R2_2.Pin_0
  N14: R2.Pin_1, Arduino1.D7
  N15: R2_2.Pin_1, Arduino1.D5
  N16: R2_3.Pin_1, Arduino1.D6

notes:
  How to charlie-plex an led matrix of 3x3 using only 6 arduino outputs. This method can be used to create or control up to a 7x7 led matrix.
  Doesnt matter what you do it will look ugly in a breadboard
  All LEDs in the matrix are addressable, meaning you can light any of them at one time with out affecting the other lights. Make them chase, dance, whatever. The way to light them is by setting one of the positive outputs to high (11 to 13) and one of the negative switching outputs to high (5 to 7). So for this matrix, to light say.. Only the second green lamp, you set outputs 11 and 6. Here is a sample of code and what lights they light (in order on breadbrd):
  digitalWrite(7,HIGH);//led 4(blue)
  digitalWrite(11,HIGH);//
  digitalWrite(6,HIGH);//led 5(blue)
  digitalWrite(13,HIGH);//
  digitalWrite(5,HIGH);//led 6(blue)
  digitalWrite(12,HIGH);//
  digitalWrite(7,HIGH);//led 7(green)
  digitalWrite(12,HIGH);//
  digitalWrite(6,HIGH);//led 8(green)
  digitalWrite(11,HIGH);//
  digitalWrite(5,HIGH);//led 9(green)
  digitalWrite(13,HIGH);//
  digitalWrite(7, HIGH);//led 1(red)
  digitalWrite(13,HIGH);
  digitalWrite(6,HIGH);//led 2(red)
  digitalWrite(12,HIGH);
  digitalWrite(5,HIGH);//led 3(red)
  digitalWrite(11,HIGH);//
  Easy to read led pin guide:
  LED : +pin : - switch pin
  Red1: 7 : 13
  Blu1 : 7 : 11
  Grn1: 7 : 12
  Red2: 6 : 12
  Blu2: 6 : 13
  Grn2: 6 : 11
  Red3: 5 : 11
  Blu3: 5 : 12
  Grn3: 5 : 13
