# Fritzing sketch id2718_Multiplexing_0 (saved by Fritzing 0.7.12b)
breadboards: 1

parts:
  Arduino1 = Arduino
  HCF_1 = HCF 4067 [package="DIP24 [THT]"]  # not connected
  R1 = Rotary Potentiometer (Small) [maximum_resistance=100kΩ]

nets:
  N1: Arduino1.+5V, R1.leg2
  N2: Arduino1.GND, R1.leg1
