# Fritzing sketch id2719_Untitled_Sketch_0 (saved by Fritzing 0.8.7b)
breadboards: 1

parts:
  U1 = prefix0000PIC16F84A
  R1 = Resistor [tolerance=±5% resistance=10k package=THT]
  XTAL1 = Crystal [frequency="4 MHz" package=SMD]
  C1 = Ceramic Capacitor [capacitance="100 nF" package="1206 [SMD, multilayer]"]
  C2 = Ceramic Capacitor [capacitance="100 nF" package="1206 [SMD, multilayer]"]
  7_Segment1 = 7 Segment Display
  R2 = Resistor [tolerance=±5% resistance=330 package=THT]
  7_Segment2 = 7 Segment Display
  R3 = Resistor [tolerance=±5% resistance=330 package=THT]
  Q2 = NPN-Transistor [package="SOT-23 [SMD]"]
  R4 = Resistor [package="2010 [SMD]"]
  R5 = Resistor [package="2010 [SMD]"]
  R6 = Resistor [package="2010 [SMD]"]
  R7 = Resistor [package="2010 [SMD]"]
  R8 = Resistor [package="2010 [SMD]"]
  R9 = Resistor [package="2010 [SMD]"]
  R10 = Resistor [package="2010 [SMD]"]
  Q1 = NPN-Transistor [part_number=2N2222 package="SOT-23 [SMD]"]
  VCC1 = 4 x AAA Battery Mount
  S1 = Pushbutton [package="[THT]"]

nets:
  N1: U1.connector3, R1.Pin_1, S1.Pin_1, S1.Pin_2
  N2: U1.connector4, C1.0, C2.1, Q2.1, Q1.1, VCC1.-, S1.Pin_3, S1.Pin_4
  N3: U1.connector5, R7.Pin_0
  N4: U1.connector6, R6.Pin_0
  N5: U1.connector7, R5.Pin_0
  N6: U1.connector8, R4.Pin_0
  N7: U1.connector9, R8.Pin_0
  N8: U1.connector10, R9.Pin_0
  N9: U1.connector11, R10.Pin_0
  N10: U1.connector13, R1.Pin_0, VCC1.+
  N11: U1.connector14, XTAL1.pin_0, C1.1
  N12: U1.connector15, XTAL1.pin_1, C2.0
  N13: U1.connector16, R2.Pin_0
  N14: U1.connector17, R3.Pin_0
  N15: 7_Segment1.Segment_E, 7_Segment2.Segment_E, R8.Pin_1
  N16: 7_Segment1.Segment_D, R4.Pin_1
  N17: 7_Segment1.common_cathode, Q1.2
  N18: 7_Segment1.Segment_C, R5.Pin_1
  N19: 7_Segment1.Segment_B, R6.Pin_1
  N20: 7_Segment1.Segment_A, R7.Pin_1
  N21: 7_Segment1.Segment_F, R9.Pin_1
  N22: 7_Segment1.Segment_G, R10.Pin_1
  N23: R2.Pin_1, Q1.0
  N24: 7_Segment2.common_cathode, Q2.2
  N25: R3.Pin_1, Q2.0
