# Fritzing sketch id271_AilgorRC_T0.1_0 (saved by Fritzing 0.9.1b)
breadboards: 1

parts:
  Composant1 = IOIO for Android
  Composant2 = USB LiPoly Charger
  U1 = LIPO-2000mAh [package=lipo-2000]
  IC1 = L293D [package=THT]
  M1 = DC Motor
  M2 = DC Motor

nets:
  N1: Composant1.PIN6, IC1.Enable_1
  N2: Composant1.PIN7, IC1.Enable_2
  N3: Composant1.PIN13, IC1.In_4
  N4: Composant1.PIN14, IC1.In_3
  N5: Composant1.5V, Composant2.VBAT, U1.+, IC1.+Vmotor, IC1.+V
  GND: Composant1.GND, Composant2.GND, U1.-, IC1.0V
  N6: Composant1.PIN38, IC1.In_1
  N7: Composant1.PIN37, IC1.In_2
  N8: IC1.Out_1_(_Controlled_by_Enable_1_), M1.pin_2
  N9: IC1.Out_2_(_Controlled_by_Enable_1_), M1.pin_1
  N10: IC1.Out_3_(_Controlled_by_Enable_2_), M2.pin_1
  N11: IC1.Out_4_(_Controlled_by_Enable_2_), M2.pin_2
