# Fritzing sketch id2720_multimeter_0 (saved by Fritzing 0.7.12b)
breadboards: 1

parts:
  R1 = resistor.fzp
  S1 = Pushbutton [package="[THT]"]
  S2 = Pushbutton [package="[THT]"]
  R2 = Resistor [tolerance=±5% resistance=220 package=THT]
  LED1 = LED - 5mm [color="Red (633nm)" package="5 mm [THT]"]
  LED2 = LED - 5mm [color="Red (633nm)" package="5 mm [THT]"]
  LED4 = LED - 5mm [color="Red (633nm)" package="5 mm [THT]"]
  LED5 = LED - 5mm [color="Red (633nm)" package="5 mm [THT]"]
  LED6 = LED - 5mm [color="Red (633nm)" package="5 mm [THT]"]
  LED7 = LED - 5mm [color="Red (633nm)" package="5 mm [THT]"]
  LED8 = LED - 5mm [color="Red (633nm)" package="5 mm [THT]"]
  Arduino1 = Arduino
  LED3 = LED - 5mm [color="Red (633nm)" package="5 mm [THT]"]
  R3 = Resistor [tolerance=±5% resistance=220 package=THT]
  R4 = Photocell (LDR) [package=THT]
  J1 = female pin header, 2 pins [form="♀ (female)"]
  R5 = Temperature Sensor (Thermistor) [thermistor_type=NTC package=THT]

nets:
  N1: R1.connector0, S1.Pin_1, S1.Pin_2, S2.Pin_3, S2.Pin_4, R2.Pin_0, Arduino1.GND
  N2: R1.connector1, LED1.anode, Arduino1.+5V, R3.Pin_0, R4.pin_1, J1.pin2, R5.pin_1
  N3: S1.Pin_3, S1.Pin_4, Arduino1.D2
  N4: S2.Pin_1, S2.Pin_2, Arduino1.D3
  N5: R2.Pin_1, LED1.cathode
  N6: LED2.cathode, Arduino1.D4
  N7: LED2.anode, LED4.anode, LED5.anode, LED6.anode, LED7.anode, LED8.anode, LED3.anode, R3.Pin_1
  N8: LED4.cathode, Arduino1.D6
  N9: LED5.cathode, Arduino1.D7
  N10: LED6.cathode, Arduino1.D8
  N11: LED7.cathode, Arduino1.D9
  N12: LED8.cathode, Arduino1.D10
  N13: Arduino1.D5, LED3.cathode
  N14: Arduino1.A0, R5.pin_0
  N15: Arduino1.A1, J1.pin1
  N16: Arduino1.A2, R4.pin_0

notes:
  Multimeter by Felix Krickl
  auswählen
  senden
  sensor
