# Fritzing sketch id2721_Multivibrator_Symmetrical_Classic_0 (saved by Fritzing 0.9.3b)
breadboards: 1

parts:
  R1 = Resistor [tolerance=±5% resistance=150k package=THT]
  R2 = Resistor [tolerance=±5% resistance=150k package=THT]
  R3 = Resistor [tolerance=±5% resistance=1k package=THT]
  R4 = Resistor [tolerance=±5% resistance=1k package=THT]
  C1 = Electrolytic Capacitor [capacitance=1µF package="100 mil [THT, electrolytic]"]
  C2 = Electrolytic Capacitor [capacitance=1µF package="100 mil [THT, electrolytic]"]
  Q1 = NPN-Transistor [package="TO92 [THT]"]
  Q2 = NPN-Transistor [package="TO92 [THT]"]
  VCC1 = 4 x AAA Battery Mount
  LED1 = LED - 5mm [color="Red (633nm)" package="5 mm [THT]"]
  LED2 = LED - 5mm [color="Green (560nm)" package="5 mm [THT]"]

nets:
  N1: R1.Pin_0, R2.Pin_0, R3.Pin_0, R4.Pin_0, VCC1.+
  N2: R1.Pin_1, C2.+, Q2.B
  N3: R2.Pin_1, C1.+, Q1.B
  N4: R3.Pin_1, LED1.anode
  N5: R4.Pin_1, LED2.anode
  N6: C1.-, Q2.C, LED2.cathode
  N7: C2.-, Q1.C, LED1.cathode
  N8: Q1.E, Q2.E, VCC1.-
