# Fritzing sketch id2723_arduino_design_man_0 (saved by Fritzing 0.9.3b)
breadboards: 1

parts:
  hc-sr1 = hc-sr04
  Part2 = Arduino Musical Instrument Shield
  Part3 = Arduino Uno (Rev3) - ICSP  # not connected

nets:
  VCC: hc-sr1.VCC, Part2.VCC
  N1: hc-sr1.Trig, Part2.TX-O
  N2: hc-sr1.Echo, Part2.RX-I
  GND: hc-sr1.GND, Part2.GND

notes:
  would need an audio player, so something to connect the music shield to using aux chord.
  This shield is used as seeedstudio v2.0 model is not available. Let RX = 0 and TX = 1
