# Fritzing sketch id2724_Arduino_music_0 (saved by Fritzing 0.9.3b)
circuit board: 8.46667cm x 5.64444cm

parts:
  Part1 = Arduino Uno (Rev3)
  SP1 = SPEAKER [package=pcb_mount_speaker]

nets:
  N1: Part1.D8, SP1.-
  N2: Part1.GND, SP1.+
