# Fritzing sketch id2724_Orhangazi44 (saved by Fritzing 0.9.0b)
breadboards: 1

parts:
  J1 = Infrared Proximity Sensor
  J2 = Infrared Proximity Sensor
  J3 = Infrared Proximity Sensor
  J4 = Infrared Proximity Sensor
  J5 = Infrared Proximity Sensor
  Part1 = Arduino Uno (Rev3)
  J6 = Basic Servo
  J7 = Basic Servo
  LED1 = LED - 5mm [color="Red (633nm)" package="5 mm [THT]"]

nets:
  N1: J1.Vout, Part1.D8
  GND: J1.GND, J2.GND, J3.GND, J4.GND, J5.GND, Part1.GND, J6.gnd, J7.gnd, LED1.cathode
  VCC: J1.Vcc, J2.Vcc, J3.Vcc, J4.Vcc, J5.Vcc, Part1.5V, J6.vcc, J7.vcc
  N2: J2.Vout, Part1.D2
  N3: J3.Vout, Part1.D4
  N4: J4.Vout, Part1.D12/MISO
  N5: J5.Vout, Part1.D7
  N6: Part1.A1, J6.pulse
  N7: Part1.A3, J7.pulse
  N8: Part1.D13/SCK, LED1.anode

notes:
  y
  x
  PIR Sensors
  LASER
