# Fritzing sketch id2725_BuzzerLCDPotenciometros_0 (saved by Fritzing 0.9.3b)
circuit board: 8.46667cm x 5.64444cm
breadboards: 1

parts:
  Componente1 = Arduino Mega 2560 (Rev3)
  R1 = Rotary Potentiometer (Small) [maximum_resistance=10kΩ package=THT]
  R2 = Rotary Potentiometer (Small) [maximum_resistance=10kΩ package=THT]
  J1 = Piezo Speaker [part_number="pasive buzzer"]
  LCD1 = LCD screen [part_number=1602]

nets:
  N1: Componente1.GND, R1.leg1, J1.pin1, LCD1.R/W, LCD1.LED-
  N2: Componente1.D13_PWM, R2.wiper
  N3: Componente1.D9_PWM, LCD1.E
  N4: Componente1.D8_PWM, LCD1.RS
  N5: Componente1.D4_PWM, LCD1.DB7
  N6: Componente1.D5_PWM, LCD1.DB6
  N7: Componente1.D6_PWM, LCD1.DB5
  N8: Componente1.D7_PWM, LCD1.DB4
  N9: R1.wiper, LCD1.V0
  N10: R1.leg2, R2.leg2, LCD1.VDD, LCD1.LED+
  N11: R2.leg1, J1.pin2
