# Fritzing sketch id2726_Musical_Bench_ver_0_0 (saved by Fritzing 0.8.7b)

parts:
  Part1 = Arduino Uno (Rev3)  # not connected
  Part2 = Arduino Musical Instrument Shield
  R3 = Resistor [tolerance=±5% resistance=1k package=THT]
  R2 = Resistor [tolerance=±5% resistance=1k package=THT]
  R1 = Resistor [tolerance=±5% resistance=39k package=THT]
  C1 = Ceramic Capacitor [capacitance=100nF package="0603 [SMD, multilayer]"]

nets:
  N1: Part2.A0, Part2.N$18, Part2.N$97, Part2.N$132, R2.Pin_0, C1.0
  N2: Part2.AREF, Part2.N$17, Part2.N$131, R1.Pin_0
  N3: Part2.GND, Part2.N$19, Part2.N$96, Part2.N$133, R3.Pin_0, C1.1
  N4: Part2.N$66, Part2.N$78, R2.Pin_1, R1.Pin_1
  N5: Part2.N$67, Part2.N$79, R3.Pin_1

notes:
  touchpad 1
  touchpad 2
