# Fritzing sketch id2727_weatherStation_0 (saved by Fritzing 0.9.2b)
breadboards: 1

parts:
  Part1 = Arduino Uno (Rev3)
  LCD1 = LCD screen
  R1 = Trimmer Potentiometer [maximum_resistance=10kΩ package=THT]
  LED1 = LED - 5mm [color="Red (633nm)" package="5 mm [THT]"]
  R2 = Resistor [tolerance=±5% resistance=220 package=THT]
  S1 = Pushbutton [package="[THT]"]
  R3 = Resistor [tolerance=±5% resistance=10k package=THT]
  R4 = Photocell (LDR) [package=THT]
  R5 = Resistor [tolerance=±5% resistance=10k package=THT]
  RHT1 = Humidity and Temperature Sensor RHT03

nets:
  N1: Part1.A0, R4.pin_0, R5.Pin_1
  N2: Part1.A1, RHT1.Data-signal
  N3: Part1.D11_PWM/MOSI, LCD1.E
  N4: Part1.D12/MISO, LCD1.RS
  N5: Part1.D2, LCD1.DB7
  N6: Part1.D3_PWM, LCD1.DB6
  N7: Part1.D4, LCD1.DB5
  N8: Part1.D5_PWM, LCD1.DB4
  N9: Part1.D7, R2.Pin_1, S1.Pin_3, S1.Pin_4, R3.Pin_1
  5V: Part1.5V, LCD1.VDD, LCD1.LED+, R1.leg2, S1.Pin_1, S1.Pin_2, R5.Pin_0, RHT1.Vcc
  GND: Part1.GND, LCD1.VSS, LCD1.R/W, LCD1.LED-, R1.leg1, LED1.cathode, R3.Pin_0, R4.pin_1, RHT1.GND_2
  N10: LCD1.V0, R1.wiper
  N11: LED1.anode, R2.Pin_0
