# Fritzing sketch id2728_MyCar_0.2_0 (saved by Fritzing 0.9.2b)
breadboards: 1

parts:
  Часть1 = Arduino Uno (Rev3)
  M1 = DC Motor
  M2 = DC Motor
  M3 = DC Motor
  M4 = DC Motor
  J1 = Basic Servo
  Часть2 = SRF05 Ultrasonic Rangefinder
  S1 = L298N Driver
  VCC2 = Battery block 9V
  VCC4 = 4 x AAA Battery Mount
  Часть3 = Bluetooth HC-05 Macho

nets:
  N1: Часть1.D8, S1.connector3
  N2: Часть1.D9_PWM, S1.connector13
  N3: Часть1.D10_PWM/SS, J1.pulse
  N4: Часть1.D11_PWM/MOSI, Часть2.connector10
  N5: Часть1.D12/MISO, Часть2.connector9
  GND: Часть1.GND, Часть2.connector11, VCC4.-, Часть3.GND
  N6: Часть1.D0/RX, Часть3.TXD
  N7: Часть1.D1/TX, Часть3.RXD
  N8: Часть1.D4, S1.connector14
  N9: Часть1.D5_PWM, S1.connector6
  N10: Часть1.D6_PWM, S1.connector5
  N11: Часть1.D7, S1.connector4
  5V: Часть1.5V, Часть2.connector8, VCC4.+, Часть3.VCC
  N12: M1.pin_1, M2.pin_1, S1.connector8
  N13: M1.pin_2, M2.pin_2, S1.connector7
  N14: M3.pin_1, M4.pin_1, S1.connector10
  N15: M3.pin_2, M4.pin_2, S1.connector9
  N16: S1.connector0, VCC2.+
  N17: S1.connector1, VCC2.-
