# Fritzing sketch id2729_myfirstfritz_0 (saved by Fritzing 0.9.2b)
breadboards: 1

parts:
  Raspberry_Pi1 = Raspberry Pi 2
  LED1 = LED - 5mm [color="Red (633nm)" package="5 mm [THT]"]
  R1 = Resistor [tolerance=±5% resistance=220 package=THT]

nets:
  3V3: Raspberry_Pi1.3v3, Raspberry_Pi1.5V, LED1.anode
  N1: Raspberry_Pi1.GND, R1.Pin_0
  N2: LED1.cathode, R1.Pin_1

notes:
  Simple Raspberry Pi 2 example
  This example will light up a red led
