# Fritzing sketch id272_AilgorRC_T0.2_0 (saved by Fritzing 0.9.1b)
breadboards: 1

parts:
  Composant1 = IOIO for Android
  Composant2 = USB LiPoly Charger
  U1 = LIPO-2000mAh [package=lipo-2000]
  IC1 = L293D [package=THT]
  M1 = DC Motor
  M2 = DC Motor

nets:
  N1: Composant1.VCC, IC1.+Vmotor
  N2: Composant1.5V, Composant2.VBAT, U1.+, IC1.+V
  GND: Composant1.GND, Composant2.GND, U1.-, IC1.0V
  N3: Composant1.PIN41, IC1.In_1
  N4: Composant1.PIN40, IC1.In_2
  N5: Composant1.PIN39, IC1.Enable_1
  N6: Composant1.PIN38, IC1.Enable_2
  N7: Composant1.PIN37, IC1.In_4
  N8: Composant1.PIN36, IC1.In_3
  N9: IC1.Out_1_(_Controlled_by_Enable_1_), M1.pin_2
  N10: IC1.Out_2_(_Controlled_by_Enable_1_), M1.pin_1
  N11: IC1.Out_3_(_Controlled_by_Enable_2_), M2.pin_1
  N12: IC1.Out_4_(_Controlled_by_Enable_2_), M2.pin_2
