# Fritzing sketch id2730_Ethernet_Photo_151125_0350_0 (saved by Fritzing 0.9.2b)
circuit board: 8.46667cm x 5.64444cm
breadboards: 1

parts:
  R1 = Photocell (LDR) [package=THT]
  R2 = Photocell (LDR) [package=THT]
  R3 = Photocell (LDR) [package=THT]
  R4 = Photocell (LDR) [package=THT]
  Part1 = Arduino Ethernet Shield (Rev3)

nets:
  N1: R1.pin_0, R3.pin_0, Part1.5V
  N2: R1.pin_1, R2.pin_0, Part1.A1
  N3: R2.pin_1, R4.pin_1, Part1.GND
  N4: R3.pin_1, R4.pin_0, Part1.A0
