# Fritzing sketch id2731_crepuscolar_alarm_0 (saved by Fritzing 0.7.11b)
breadboards: 1

parts:
  Arduino1 = Arduino
  J1 = Piezo Speaker
  R1 = Photocell (LDR) [package=THT]
  LED1 = LED - 5mm [color="Green (555nm)" package="5 mm [THT]"]
  LED2 = LED - 5mm [color="Green (555nm)" package="5 mm [THT]"]
  LED3 = LED - 5mm [color="Green (555nm)" package="5 mm [THT]"]
  R2 = Resistor [tolerance=±5% resistance=220 package=THT]
  R3 = Resistor [tolerance=±5% resistance=220 package=THT]
  R4 = Resistor [tolerance=±5% resistance=220 package=THT]
  R5 = Resistor [tolerance=±5% resistance=100 package=THT]
  R6 = Resistor [tolerance=±5% resistance=10k package=THT]

nets:
  N1: Arduino1.GND, J1.pin1, LED1.cathode, LED2.cathode, LED3.cathode, R6.Pin_1
  N2: Arduino1.D5, R5.Pin_1
  N3: Arduino1.D4, R4.Pin_1
  N4: Arduino1.D3, R3.Pin_1
  N5: Arduino1.D2, R2.Pin_1
  N6: Arduino1.+5V, R1.pin_0
  N7: Arduino1.A0, R1.pin_1, R6.Pin_0
  N8: J1.pin2, R5.Pin_0
  N9: LED1.anode, R2.Pin_0
  N10: LED2.anode, R4.Pin_0
  N11: LED3.anode, R3.Pin_0
