# Fritzing sketch id2732_Untitled_Sketch_0 (saved by Fritzing 0.9.3b)
breadboards: 1

parts:
  U1 = 2ChannelRelay
  U2 = MIC [package=mic-9.7mm]
  Part1 = Arduino Uno (Rev3)
  LED1 = RGB LED (com. cathode, rbg) [package="5 mm [THT]"]
  R1 = Resistor [tolerance=±5% resistance=220 package="0402 [SMD]"]
  R2 = Resistor [tolerance=±5% resistance=220 package="0402 [SMD]"]
  R3 = Resistor [tolerance=±5% resistance=220 package="0402 [SMD]"]

nets:
  N1: U1.connector0, Part1.5V
  N2: U1.connector1, U2.2, Part1.GND, LED1.common_cathode
  N3: U1.connector2, Part1.D7
  N4: U1.connector3, Part1.D8
  N5: U2.1, Part1.A0
  N6: Part1.D11_PWM/MOSI, R3.Pin_1
  N7: Part1.D12/MISO, R2.Pin_1
  N8: Part1.D13/SCK, R1.Pin_1
  N9: LED1.red_anode, R1.Pin_0
  N10: LED1.blue_anode, R2.Pin_0
  N11: LED1.green_anode, R3.Pin_0
