# Fritzing sketch id2733_ir_0 (saved by Fritzing 0.9.3b)
breadboards: 2

parts:
  J1 = Infrared Proximity Sensor  # not connected
  Part1 = Arduino Uno (Rev3)
  C1 = Electrolytic Capacitor [capacitance=1µF package="100 mil [THT, electrolytic]"]  # not connected
  R1 = Resistor [tolerance=±5% resistance=230 package=THT]
  U1 = Vibration Motor- ROB-08449 [package=vibe-motor-10mm]
  R2 = Resistor [tolerance=±5% resistance=230 package=THT]
  LED1 = LEDs [package=led10mm]

nets:
  N1: Part1.D4, R1.Pin_0
  N2: Part1.GND, U1.+, LED1.A
  N3: R1.Pin_1, U1.-, R2.Pin_0
  N4: R2.Pin_1, LED1.C

notes:
  I plan to do this, including the other breadboard
