# Fritzing sketch id2735_Arduino_Projects_Book___Project_7___Keyboard_Instrument_0 (saved by Fritzing 0.9.2b)
breadboards: 1

parts:
  Part1 = Arduino Uno (Rev3)
  J1 = Piezo Speaker
  S1 = Pushbutton [package="[THT]"]
  S2 = Pushbutton [package="[THT]"]
  S3 = Pushbutton [package="[THT]"]
  S4 = Pushbutton [package="[THT]"]
  R1 = Resistor [tolerance=±5% resistance=220 package=THT]
  R2 = Resistor [tolerance=±5% resistance=10k package=THT]
  R3 = Resistor [tolerance=±5% resistance=1M package=THT]
  R4 = Resistor [tolerance=±5% resistance=10k package=THT]
  VCC1 = Battery block 9V  # not connected

nets:
  N1: Part1.A0, S1.Pin_3, S1.Pin_4, S2.Pin_3, S2.Pin_4, S3.Pin_3, S3.Pin_4, S4.Pin_3, S4.Pin_4, R4.Pin_1
  N2: Part1.D8, J1.pin1
  N3: Part1.5V, S1.Pin_1, S1.Pin_2, R1.Pin_0, R3.Pin_0
  N4: Part1.GND, J1.pin2, R4.Pin_0
  N5: S2.Pin_1, S2.Pin_2, R1.Pin_1
  N6: S3.Pin_1, S3.Pin_2, R2.Pin_1
  N7: S4.Pin_1, S4.Pin_2, R3.Pin_1
