# Fritzing sketch id2738_Ext_Relay_Shield_0 (saved by Fritzing 0.8.5b)
circuit board: 6.88566cm x 5.36311cm
breadboards: 1

parts:
  J8 = female pin header, 8 pins [form="♀ (female)"]
  J9 = female pin header, 6 pins [form="♀ (female)"]
  J10 = female pin header, 6 pins [form="♀ (female)"]
  J11 = female pin header, 8 pins [form="♀ (female)"]
  DIODE1 = Rectifier Diode [part_number=1N4001 package="300 mil [THT]"]
  DIODE2 = Rectifier Diode [part_number=1N4001 package="300 mil [THT]"]
  8050 = NPN-Transistor [package="TO92 [THT]"]
  8050_2 = NPN-Transistor [package="TO92 [THT]"]
  J16 = double row female pin header, 20 pins [form="♀ (female)"]
  LED1 = LED - 3mm [color="Red (633nm)" package="3 mm [THT]"]
  LED2 = LED - 3mm [color="Red (633nm)" package="3 mm [THT]"]
  R1 = Resistor [tolerance=±5% resistance=220 package=THT]
  R2 = Resistor [tolerance=±5% resistance=220 package=THT]
  J18 = female pin header, 2 pins [form="♀ (female)"]
  S1 = Pushbutton [package="[THT]"]
  R3 = Resistor [tolerance=±5% resistance=220 package=THT]
  R4 = Resistor [tolerance=±5% resistance=220 package=THT]
  J21 = female pin header, 2 pins [form="♀ (female)"]
  J14 = screw terminal, 3 pins  # not connected
  J15 = screw terminal, 3 pins  # not connected
  J19 = screw terminal, 2 pins
  J20 = screw terminal, 2 pins

nets:
  N1: J8.pin2, S1.Pin_3, S1.Pin_4
  N2: J8.pin3, J16.pin7
  N3: J8.pin4, J16.pin6
  N4: J8.pin5, J16.pin5
  N5: J8.pin6, J16.pin4
  N6: J8.pin7, J16.pin3
  N7: J8.pin8, J16.pin2
  N8: J9.pin1, S1.Pin_1, S1.Pin_2
  N9: J9.pin3, DIODE1.cathode, DIODE2.cathode, J19.pin2, J20.pin2
  N10: J9.pin4, J9.pin5, 8050.E, 8050_2.E, R3.Pin_1, R4.Pin_1
  N11: J10.pin1, J16.pin8
  N12: J10.pin2, J16.pin9
  N13: J10.pin3, J16.pin10
  N14: J10.pin4, J16.pin11
  N15: J10.pin5, J16.pin12
  N16: J10.pin6, J16.pin13
  N17: J11.pin1, J16.pin1
  N18: J11.pin2, J16.pin20
  N19: J11.pin3, J16.pin19
  N20: J11.pin4, J16.pin18
  N21: J11.pin5, J16.pin17
  N22: J11.pin6, J16.pin16
  N23: J11.pin7, J16.pin15
  N24: J11.pin8, J16.pin14
  N25: DIODE1.anode, 8050_2.C
  N26: DIODE2.anode, 8050.C
  N27: 8050.B, LED1.cathode
  N28: 8050_2.B, LED2.cathode
  N29: LED1.anode, R1.Pin_1
  N30: LED2.anode, R2.Pin_1
  N31: R1.Pin_0, J18.pin1
  N32: R2.Pin_0, J18.pin2
  N33: R3.Pin_0, J21.pin1, J20.pin1
  N34: R4.Pin_0, J21.pin2, J19.pin1
