# Fritzing sketch id2739_3.3vArduino1.7inchNetLabels_0 (saved by Fritzing 0.9.0b)
circuit board: 7cm x 4.3cm
breadboards: 1

parts:
  S1 = Momentary Switch [package=tactile-pth]
  FTDI = male pin header, 6 pins [form="♂ (male)"]
  AtMega_328 = MICROCONTROLLER [package=dil28-3]
  nrf24 = double row female pin header, 8 pins [form="♀ (female)"]
  3_3V = V_REG_MIC2920 [package=sot223]
  5V = V_REG_MIC2920 [package=sot223]
  BSS138Dw2 = dualN-channelMosfet
  BSS138Dw1 = dualN-channelMosfet
  C3 = Ceramic Capacitor [capacitance=0.1µF package="0603 [SMD, multilayer]"]
  R1 = Resistor [tolerance=±5% resistance=10k package="1206 [SMD]"]
  Y2_8MHz = Resonator [package=resonator-smd]
  R2 = Resistor [tolerance=±5% resistance=750 package="0603 [SMD]"]
  SCK_LED = smd LED [color="Green (565nm)" package="0603 [SMD]"]
  R3 = Resistor [tolerance=±5% resistance=750 package="0603 [SMD]"]
  C7 = Ceramic Capacitor [capacitance=0.1µF voltage=20V package="0603 [SMD, multilayer]"]
  Vin_7-12V = Screw terminal - 2 pins [package=THT]
  DIO_5V = screw terminal, 6 pins
  DIO_3_3V = screw terminal, 10 pins
  C1 = Ceramic Capacitor [capacitance=10µF package="1206 [SMD, multilayer]"]
  C2 = Ceramic Capacitor [capacitance=0.1µF package="0603 [SMD, multilayer]"]
  C5 = Ceramic Capacitor [capacitance=0.1µF voltage=16V package="0603 [SMD, multilayer]"]
  C4 = Ceramic Capacitor [capacitance=10µF voltage=16V package="1206 [SMD, multilayer]"]
  C6 = Ceramic Capacitor [capacitance=10µF voltage=16V package="1206 [SMD, multilayer]"]
  Analog_3_3V = screw terminal, 8 pins
  PWR = smd LED [color="Red (633nm)" package="0603 [SMD]"]

nets:
  GND: S1.1, S1.2, FTDI.pin5, FTDI.pin6, AtMega_328.GND, AtMega_328.AGND, nrf24.pin1, 3_3V.GND, 5V.GND, C3.0, Y2_8MHz.2, SCK_LED.cathode, Vin_7-12V.pin1, DIO_5V.pin6, DIO_3_3V.pin1, C1.0, C2.0, C5.1, C4.1, C6.0, Analog_3_3V.pin2, PWR.cathode
  N1: S1.3, S1.4, AtMega_328.PC6(_RESET), R1.Pin_0, C7.1
  DTR: FTDI.pin1, C7.0
  D1: FTDI.pin2, AtMega_328.PD1(TXD), BSS138Dw1.connector4, DIO_3_3V.pin9
  D0: FTDI.pin3, AtMega_328.PD0(RXD), BSS138Dw1.connector1, DIO_3_3V.pin10
  3.3V: FTDI.pin4, AtMega_328.VCC, AtMega_328.AVCC, nrf24.pin8, 3_3V.OUT, BSS138Dw2.connector2, BSS138Dw2.connector5, BSS138Dw1.connector2, BSS138Dw1.connector5, R1.Pin_1, R2.Pin_0, DIO_3_3V.pin2, C1.1, C2.1, Analog_3_3V.pin1
  IRQ: AtMega_328.PD2(INT0), nrf24.pin5
  D3: AtMega_328.PD3(INT1), BSS138Dw2.connector1, DIO_3_3V.pin8
  D4: AtMega_328.PD4(XCK_T0), BSS138Dw2.connector4, DIO_3_3V.pin7
  N2: AtMega_328.PB6(XTAL1_TOSC1), Y2_8MHz.1
  N3: AtMega_328.PB7(XTAL2_TOSC2), Y2_8MHz.3
  D5: AtMega_328.PD5(T1), DIO_3_3V.pin6
  D6: AtMega_328.PD6(AIN0), DIO_3_3V.pin5
  D7: AtMega_328.PD7(AIN1), DIO_3_3V.pin4
  D8: AtMega_328.PB0(ICP), DIO_3_3V.pin3
  CE: AtMega_328.PB1(OC1A), nrf24.pin2
  CS: AtMega_328.PB2(SS_OC1B), nrf24.pin7
  MOSI: AtMega_328.PB3(MOSI_OC2), nrf24.pin6
  MISO: AtMega_328.PB4(MISO), nrf24.pin4
  SCK: AtMega_328.PB5(SCK), nrf24.pin3, R3.Pin_0
  N4: AtMega_328.AREF, C3.1
  AD0: AtMega_328.PC0(ADC0), Analog_3_3V.pin8
  AD1: AtMega_328.PC1(ADC1), Analog_3_3V.pin7
  AD2: AtMega_328.PC2(ADC2), Analog_3_3V.pin6
  AD3: AtMega_328.PC3(ADC3), Analog_3_3V.pin5
  AD4: AtMega_328.PC4(ADC4_SDA), Analog_3_3V.pin4
  AD5: AtMega_328.PC5(ADC5_SCL), Analog_3_3V.pin3
  12V: 3_3V.IN, 5V.IN, Vin_7-12V.pin2, C6.1
  5V: 5V.OUT, DIO_5V.pin5, C5.0, C4.0
  N5: BSS138Dw2.connector3, DIO_5V.pin1
  N6: BSS138Dw2.connector6, DIO_5V.pin2
  N7: BSS138Dw1.connector3, DIO_5V.pin3
  N8: BSS138Dw1.connector6, DIO_5V.pin4
  N9: R2.Pin_1, PWR.anode
  N10: SCK_LED.anode, R3.Pin_1

notes:
  DTR
  TXO
  VCC
  CTS
  RXI
  GND
  D1 5V
  D2 5V
  5V
  D5 5V
  D4 5V
  D4 3.3V
  3.3V
  D8 3.3V
  D7 3.3V
  D6 3.3V
  D5 3.3V
  D3 3.3V
  D1 3.3V
  D0 3.3V
  D8
  D7
  D6
  D5
  D4
  D3
  D1
  D0
  V+
  3.3V Arduino Clone set up for Mysenors.org, Rev1
  AD1
  AD2
  AD3
  AD4
  AD5
  MySensors Node
  Rev. 1.0
  AD0
