# Fritzing sketch id273_shield_full_rect_DIN4M_v1_3_1_0 (saved by Fritzing 0.9.3b)
circuit board: 5.33cm x 6.6cm
breadboards: 1

parts:
  OW3 = mystery part, 3 pins [chip_label=TEMPUSR2]
  OW4 = mystery part, 3 pins [chip_label=TEMPUSR1]
  MH&USR = mystery part, 4 pins [chip_label=SW1-3]
  RHT1 = Humidity and Temperature Sensor RHT03
  R1 = Resistor [tolerance=±5% resistance=220 package=THT]
  R2 = Resistor [tolerance=±5% resistance=470 package=THT]
  R3 = Resistor [tolerance=±5% resistance=470 package=THT]
  R4 = Resistor [tolerance=±5% resistance=470 package=THT]
  R5 = Resistor [tolerance=±5% resistance=1.0k package=THT]
  R7 = Resistor [tolerance=±5% resistance=4.7k package=THT]
  R6 = Resistor [tolerance=±5% resistance=4.7k package=THT]
  R8 = Resistor [tolerance=±5% resistance=4.7k package=THT]
  R9 = Resistor [tolerance=±5% resistance=4.7k package=THT]
  solar_board = shrouded pin header, 6 pins [form="♂ (shrouded male)"]
  Part1 = Arduino Yun
  LED4 = LED - 3mm [color="Blue (505nm)" package="3 mm [THT]"]
  LED2 = LED - 3mm [color="Yellow (595nm)" package="3 mm [THT]"]
  LED3 = LED - 3mm [color="Red (633nm)" package="3 mm [THT]"]
  LED1 = LED - 3mm [color="White (6500K)" package="3 mm [THT]"]
  VEXT-5VREG = mystery part, 2 pins [chip_label="V EXT"]
  C1 = Electrolytic Capacitor [capacitance=10µF package="100 mil [THT, electrolytic]"]
  C2 = Ceramic Capacitor [capacitance=0.1nF package="100 mil [THT, multilayer]"]
  RESET = Pushbutton [package="[THT]"]

nets:
  N1: OW3.pin2, R7.Pin_1, Part1.D6_PWM
  VCC: OW3.pin3, OW4.pin3, MH&USR.pin4, RHT1.Vcc, R5.Pin_0, R7.Pin_0, R6.Pin_0, R8.Pin_0, R9.Pin_0, solar_board.pin3, Part1.5V
  N2: OW4.pin2, R6.Pin_1, Part1.D7
  N3: MH&USR.pin2, R3.Pin_0, Part1.D8
  N4: MH&USR.pin3, R4.Pin_0, Part1.ICSP_MISO, Part1.D12/MISO
  N5: RHT1.Data-signal, R5.Pin_1, Part1.D2
  N6: R1.Pin_0, Part1.D3_PWM
  N7: R1.Pin_1, LED1.anode
  N8: R2.Pin_0, solar_board.pin2, Part1.D9_PWM
  N9: R2.Pin_1, LED2.anode
  N10: R3.Pin_1, LED3.anode
  N11: R4.Pin_1, LED4.anode
  N12: R8.Pin_1, solar_board.pin4, Part1.D4
  N13: R9.Pin_1, solar_board.pin6, Part1.D5_PWM
  N14: Part1.RESET, RESET.Pin_1, RESET.Pin_2
  N15: Part1.VIN, VEXT-5VREG.pin2, C1.+, C2.1
  N16: RESET.Pin_3, RESET.Pin_4

notes:
  +
  U
  H
  D
  renergia.fr
  ASC-Kit v1.3
