# Fritzing sketch id2740_Untitled_Sketch_0 (saved by Fritzing 0.7.11b)

parts:
  Arduino1 = Arduino
  J1 = Basic Servo
  VCC1 = Battery  # not connected
  VCC2 = Battery  # not connected

nets:
  N1: Arduino1.D9, Arduino1.D8, Arduino1.D7, Arduino1.D6, Arduino1.D5, Arduino1.D4, Arduino1.D3, Arduino1.D2, J1.pulse

notes:
  8x
  4 v
  9v
  I'm using 8 servos on pins 2-9. I just show them hooking up to one servo for illustrational purposes. All 8 servos will be hooked up in this manner.
