# Fritzing sketch id2741_sterowanie_serwem_schemat_0 (saved by Fritzing 0.7.7b)
breadboards: 1

parts:
  Arduino = Arduino
  servo = Basic Servo
  potencjometr = Rotary Potentiometer (Small) [maximum_resistance=100kΩ]

nets:
  GND: Arduino.GND, servo.gnd, potencjometr.leg1
  N1: Arduino.D9, servo.pulse
  VIN: Arduino.VIN, servo.vcc
  N2: Arduino.A0, potencjometr.wiper
