# Fritzing sketch id2742_Traffic_Light_Project_Schematic_0 (saved by Fritzing 0.9.2b)
breadboards: 2

parts:
  Part1 = Arduino Uno (Rev3)
  U1 = Packages: [package=dil28-3]
  R1 = Resistor [tolerance=±5% resistance=2.2k package=THT]
  LED1 = smd LED [color="Red (633nm)" package="1206 [SMD]"]
  LED2 = smd LED [color="Yellow (595nm)" package="1206 [SMD]"]
  LED3 = smd LED [color="Green (555nm)" package="1206 [SMD]"]
  LED4 = smd LED [color="Red (633nm)" package="1206 [SMD]"]
  LED5 = smd LED [color="Yellow (595nm)" package="1206 [SMD]"]
  LED6 = smd LED [color="Green (555nm)" package="1206 [SMD]"]
  LED7 = smd LED [color="Red (633nm)" package="1206 [SMD]"]
  LED8 = smd LED [color="Yellow (595nm)" package="1206 [SMD]"]
  LED9 = smd LED [color="Green (555nm)" package="1206 [SMD]"]
  LED10 = smd LED [color="Red (633nm)" package="1206 [SMD]"]
  LED11 = smd LED [color="Yellow (595nm)" package="1206 [SMD]"]
  LED12 = smd LED [color="Green (555nm)" package="1206 [SMD]"]
  LED13 = LEDs [package=led10mm]
  LED14 = LEDs [package=led10mm]
  LED15 = LEDs [package=led10mm]
  LED16 = LEDs [package=led10mm]
  S1 = Pushbutton [package="[THT]"]
  S2 = Pushbutton [package="[THT]"]
  S3 = Pushbutton [package="[THT]"]
  S4 = Pushbutton [package="[THT]"]

nets:
  N1: Part1.D9_PWM, U1.XLAT
  N2: Part1.D10_PWM/SS, U1.BLANK
  N3: Part1.D11_PWM/MOSI, U1.SIN
  N4: Part1.D13/SCK, U1.SCLK
  GND: Part1.GND, U1.GND, U1.VPRG, R1.Pin_1, S1.Pin_1, S1.Pin_2, S2.Pin_1, S2.Pin_2, S3.Pin_1, S3.Pin_2, S4.Pin_1, S4.Pin_2
  N5: Part1.D3_PWM, U1.GSCLK
  N6: Part1.D4, S1.Pin_3, S1.Pin_4
  N7: Part1.D5_PWM, S4.Pin_3, S4.Pin_4
  N8: Part1.D6_PWM, S2.Pin_3, S2.Pin_4
  N9: Part1.D7, S3.Pin_3, S3.Pin_4
  5V: Part1.5V, U1.DCPRG, U1.VCC, LED1.anode, LED2.anode, LED3.anode, LED4.anode, LED5.anode, LED6.anode, LED7.anode, LED8.anode, LED9.anode, LED10.anode, LED11.anode, LED12.anode, LED13.C, LED14.C, LED15.C, LED16.C
  N10: U1.OUT1, LED6.cathode, LED9.cathode
  N11: U1.OUT2, LED5.cathode, LED8.cathode
  N12: U1.OUT3, LED4.cathode, LED7.cathode
  N13: U1.OUT4, LED3.cathode, LED12.cathode
  N14: U1.OUT5, LED2.cathode, LED11.cathode
  N15: U1.OUT6, LED1.cathode, LED10.cathode
  N16: U1.OUT7, LED15.A
  N17: U1.OUT8, LED16.A
  N18: U1.OUT9, LED14.A
  N19: U1.OUT10, LED13.A
  N20: U1.XERR, U1.IREF, R1.Pin_0
