# Fritzing sketch id2743_migavac_0 (saved by Fritzing 0.7.10b)
breadboards: 1

parts:
  Q1 = NPN-Transistor [part_number=2n3904 package="TO92 [THT]"]
  Q2 = NPN-Transistor [part_number=2n3904 package="TO92 [THT]"]
  R1 = Resistor [tolerance=±5% resistance=220 package=THT]
  R3 = Resistor [tolerance=±5% resistance=100k package=THT]
  R4 = Resistor [tolerance=±5% resistance=100k package=THT]
  C1 = Electrolytic Capacitor [capacitance=47µF package="100 mil [THT, electrolytic]"]
  C2 = Electrolytic Capacitor [capacitance=47µF package="100 mil [THT, electrolytic]"]
  VCC1 = Battery
  LED2 = LED - 5mm [color="Green (565nm)" package="5 mm [THT]"]
  LED3 = LED - 5mm [color="Red (633nm)" package="5 mm [THT]"]
  R5 = Resistor [tolerance=±5% resistance=220 package=THT]

nets:
  N1: Q1.E, Q2.E, VCC1.-
  N2: Q1.B, R3.Pin_1, C2.-
  N3: Q1.C, R1.Pin_1, C1.+
  N4: Q2.B, R4.Pin_1, C1.-
  N5: Q2.C, C2.+, R5.Pin_1
  N6: R1.Pin_0, LED2.cathode
  N7: R3.Pin_0, R4.Pin_0, VCC1.+, LED2.anode, LED3.anode
  N8: LED3.cathode, R5.Pin_0
