# Fritzing sketch id2746_MyFirstProjectGulevski_0 (saved by Fritzing 0.9.3b)
breadboards: 1

parts:
  U1 = Voltage Regulator - 5V [package="TO220 [THT]"]
  VCC1 = Battery  # not connected
  LED1 = LED - 5mm [color="Red (633nm)" package="5 mm [THT]"]  # not connected
  R1 = Resistor [tolerance=±5% resistance=220 package=THT]
  S1 = Toggle Switch [package=THT]

nets:
  N1: U1.input_voltage, S1.COM
  N2: U1.GND, R1.Pin_0
  N3: U1.output_voltage, R1.Pin_1
