# Fritzing sketch id2747_Untitled_Sketch_2_0 (saved by Fritzing 0.9.2b)
breadboards: 1

parts:
  Part1 = Arduino Uno (Rev3)
  LED1 = LED - 5mm [color="Red (633nm)" package="5 mm [THT]"]
  R1 = Resistor [tolerance=±5% resistance=220 package="2010 [SMD]"]
  S1 = Pushbutton [package="[SMD]"]
  R2 = Resistor [tolerance=±5% resistance=220 package="2010 [SMD]"]

nets:
  N1: Part1.D8, S1.Pin_3, S1.Pin_4, R2.Pin_0
  N2: Part1.D3_PWM, R1.Pin_1
  N3: Part1.5V, S1.Pin_1, S1.Pin_2
  N4: Part1.GND, R2.Pin_1
  N5: LED1.anode, R1.Pin_0
