# Fritzing sketch id2748_V1_NW_MySensors_0 (saved by Fritzing 0.9.3b)
breadboards: 1

parts:
  HLK-PM1 = HLK-PM01
  U1 = LMZ14203 [package=to-pmod-7]
  Onderdeel1 = Arduino Pro Mini (3.3V)

nets:
  GND: HLK-PM1.-Vo, U1.GND, Onderdeel1.GND
  N1: HLK-PM1.+Vo, U1.VIN
  N2: U1.VOUT, Onderdeel1.VCC
