# Fritzing sketch id2749_RaspberryPiGateway_0 (saved by Fritzing 0.9.3b)

parts:
  Part1 = NRF24L01+ Breakout Board
  Raspberry_Pi1 = Raspberry Pi 2

nets:
  GND: Part1.GND, Raspberry_Pi1.GND
  VCC: Part1.VCC, Raspberry_Pi1.3v3
  N1: Part1.CE, Raspberry_Pi1.GPIO25
  N2: Part1.CS, Raspberry_Pi1.GPIO8
  N3: Part1.SCK, Raspberry_Pi1.GPIO11
  N4: Part1.MOSI, Raspberry_Pi1.GPIO10
  N5: Part1.MISO, Raspberry_Pi1.GPIO9
