# Fritzing sketch id274_Schema_bombe_0 (saved by Fritzing 0.9.3b)
breadboards: 3

parts:
  Composant1 = Arduino Uno (Rev3)
  LCD1 = LCD screen
  KEYPAD1 = Membrane_Matrix_Keypad
  potentiometre_100kOhm = Trimmer Potentiometer [maximum_resistance=10kΩ package=THT]  # not connected
  Buzzer_5v = Piezo Speaker
  6kOhm = Resistor [tolerance=±5% resistance=220 package=THT]
  6kOhm_2 = Resistor [tolerance=±5% resistance=220 package=THT]
  6kOhm_3 = Resistor [tolerance=±5% resistance=220 package=THT]
  6kOhm_4 = Resistor [tolerance=±5% resistance=220 package=THT]
  Prise_jst_3_pin_(module_pour_faire_exploser) = jst 3-pin
  Prise_jst_(module_pour_desamorcer) = jst 3-pin
  Relay = RELAY [package=relay-jzc]
  Sirène_12v = Loudspeaker
  Alimentation_12V = Battery block 9V  # not connected
  Prise_jst_4_pin_(module_alerte_d'explosion) = Header 4 [package=jst-4-pth]
  Prise_jst_4_pin_(module_alerte_de_desamorçage) = Header 4 [package=jst-4-pth]
  Prise_jst_4_pin_(Fiche_module_complémentaire) = Header 4 [package=jst-4-pth]
  Intérupteur_à_clef_de_mise_sous_tension = SWITCH_SPDT [package=kps-1290]
  Fusible_10A = FUSE [package=fuse_5mm]

nets:
  N1: Composant1.D8, KEYPAD1.connector6
  N2: Composant1.D9_PWM, KEYPAD1.connector5
  N3: Composant1.D10_PWM/SS, KEYPAD1.connector4
  N4: Composant1.D11_PWM/MOSI, KEYPAD1.connector3
  N5: Composant1.D12/MISO, KEYPAD1.connector2
  N6: Composant1.D13/SCK, KEYPAD1.connector1
  N7: Composant1.GND, Buzzer_5v.pin1, 6kOhm.Pin_0, 6kOhm_2.Pin_0, 6kOhm_3.Pin_0, 6kOhm_4.Pin_0, Prise_jst_3_pin_(module_pour_faire_exploser).connector5, Prise_jst_(module_pour_desamorcer).connector5, Relay.MAIN, Prise_jst_4_pin_(module_alerte_d'explosion).4, Prise_jst_4_pin_(module_alerte_de_desamorçage).4, Prise_jst_4_pin_(Fiche_module_complémentaire).4
  N8: Composant1.D0/RX, Prise_jst_4_pin_(Fiche_module_complémentaire).1
  N9: Composant1.D1/TX, Prise_jst_4_pin_(Fiche_module_complémentaire).2
  N10: Composant1.D2, 6kOhm_4.Pin_1, Prise_jst_4_pin_(module_alerte_de_desamorçage).2
  N11: Composant1.D3_PWM, 6kOhm_3.Pin_1, Relay.COIL1, Prise_jst_4_pin_(module_alerte_d'explosion).2
  N12: Composant1.D4, 6kOhm_2.Pin_1, Prise_jst_(module_pour_desamorcer).connector7
  N13: Composant1.D5_PWM, 6kOhm.Pin_1, Prise_jst_3_pin_(module_pour_faire_exploser).connector7
  N14: Composant1.D7, KEYPAD1.connector7
  N15: Composant1.VIN, Relay.NC, Prise_jst_4_pin_(module_alerte_d'explosion).1, Prise_jst_4_pin_(module_alerte_de_desamorçage).1, Intérupteur_à_clef_de_mise_sous_tension.P
  N16: LCD1.VDD, Prise_jst_3_pin_(module_pour_faire_exploser).connector6, Prise_jst_(module_pour_desamorcer).connector6, Prise_jst_4_pin_(module_alerte_d'explosion).3, Prise_jst_4_pin_(module_alerte_de_desamorçage).3, Prise_jst_4_pin_(Fiche_module_complémentaire).3
  N17: Relay.COIL2, Sirène_12v.pin2
  N18: Intérupteur_à_clef_de_mise_sous_tension.S, Fusible_10A.2
