# Fritzing sketch id2750_NChannelwitch___ATMega_0 (saved by Fritzing 0.7.4b)
breadboards: 1

parts:
  U1 = atmega328 [package=dip]
  LED1 = LED - 5mm [color="Red (633nm)" package="5 mm [THT]"]
  R1 = Resistor [tolerance=±5% resistance=220 package=THT]
  R4 = Resistor [tolerance=±5% resistance=220 package=THT]
  U3 = Voltage Regulator - Variable [package="TO220 [THT]"]
  C2 = Electrolytic Capacitor [capacitance=1µF package="100 mil [THT, electrolytic]"]
  C3 = Electrolytic Capacitor [capacitance=1µF package="100 mil [THT, electrolytic]"]
  Power_plug2 = Power plug
  S1 = Pushbutton [package="[THT]"]
  J1 = male pin header, 6 pins [form="♂ (male)"]
  J2 = male pin header, 8 pins [form="♂ (male)"]
  J3 = male pin header, 8 pins [form="♂ (male)"]
  J4 = male pin header, 6 pins [form="♂ (male)"]
  J5 = male pin header, 2 pins [form="♂ (male)"]

nets:
  N1: U1.RESET, R4.Pin_1, S1.Pin_1, S1.Pin_2
  N2: U1.D0_(RX), J2.pin1
  N3: U1.D1_(TX), J2.pin2
  N4: U1.D2, J2.pin3
  N5: U1.D3_(PWM), J2.pin4
  N6: U1.D4, J2.pin5
  N7: U1.VCC, U1.AVCC, U1.AREF, R4.Pin_0, U3.IN, C2.+, J4.pin1, J4.pin2, J4.pin3, J4.pin4, J4.pin5, J4.pin6
  GND: U1.GND, LED1.anode, U3.OUT, C2.-, C3.+, Power_plug2.GND, S1.Pin_3, S1.Pin_4, J3.pin1, J3.pin2, J3.pin3, J3.pin4, J3.pin5, J3.pin6, J3.pin7, J3.pin8
  N8: U1.XLAT1, R1.Pin_0
  N9: U1.D5_(PWM), J2.pin6
  N10: U1.D6_(PWM), J2.pin7
  N11: U1.D7, J2.pin8
  N12: U1.D8, J1.pin6
  N13: U1.D9_(PWM), J1.pin5
  N14: U1.D10_(PWM), J1.pin4
  N15: U1.D11_(PWM), J1.pin3
  N16: U1.D12, J1.pin2
  N17: U1.D13, J1.pin1
  N18: U1.A2, J5.pin2
  N19: U1.A3, J5.pin1
  N20: LED1.cathode, R1.Pin_1
  N21: U3.ADJ, C3.-, Power_plug2.VCC
