# Fritzing sketch id2752_nanogrammer_0 (saved by Fritzing 0.7.5b)
breadboards: 1

parts:
  + = LED - 5mm [color="Red (633nm)" package="5 mm [THT]"]
  220Ω = Resistor [tolerance=±5% resistance=220 package=THT]
  ATtiny = attiny85 [package=dip]
  * = Arduino Nano v2.3
  | = Electrolytic Capacitor [capacitance=1µF package="100 mil [THT, electrolytic]"]

nets:
  N1: +.cathode, ATtiny.Pin_5, *.D11, |.-
  N2: +.anode, 220Ω.Pin_0
  N3: 220Ω.Pin_1, ATtiny.Pin_8, *.+5V
  N4: ATtiny.Pin_1, *.D10
  N5: ATtiny.Pin_4, *.GND
  N6: ATtiny.Pin_6, *.D12
  N7: ATtiny.Pin_7, *.D13
  N8: *.RST, |.+

notes:
  D11
  D12
  D10
  D13
