# Fritzing sketch id2753_Datalogger_NANO_DHT11_SDcard_0 (saved by Fritzing 0.9.3b)
breadboards: 1

parts:
  Componente1 = MicroSD Card Module
  Componente2 = SHT1x-Breakout
  Componente3 = Arduino Nano (Rev3.0) (ICSP)
  Componente4 = SHT1x-Breakout

nets:
  GND: Componente1.GND, Componente2.GND, Componente3.GND, Componente4.GND
  VCC: Componente1.VCC, Componente2.VCC, Componente3.5V, Componente4.VCC
  N1: Componente1.MISO, Componente3.D12/MISO
  N2: Componente1.MOSI, Componente3.D11/MOSI
  N3: Componente1.SCK, Componente3.D13/SCK
  N4: Componente1.CS, Componente3.D4
  N5: Componente2.DATA, Componente3.D2
  N6: Componente3.D3, Componente4.DATA

notes:
  Semplicissimo Data Logger con due sensori DHT11 ed una shield microSD collegati su Arduino Nano
