# Fritzing sketch id2754_Nano_light_theremin_0 (saved by Fritzing 0.9.3b)
breadboards: 1

parts:
  Part1 = Arduino Nano (Rev3.0)
  J1 = Piezo Speaker
  R1 = Resistor [tolerance=±5% resistance=220 package=THT]
  R2 = Photocell (LDR) [package=THT]

nets:
  N1: Part1.GND, J1.pin1
  N2: Part1.5V, R2.pin_0
  N3: Part1.A0, R1.Pin_0, R2.pin_1
