# Fritzing sketch id2755_1_0 (saved by Fritzing 0.9.3b)
breadboards: 1

parts:
  Часть2 = Arduino Nano (Rev3.0)
  Часть3 = adafruit [part_number=938]
  R1 = Temperature Sensor (Thermistor) [thermistor_type=NTC package=THT]
  R2 = Resistor [tolerance=±5% resistance=220 package=THT]

nets:
  N1: Часть2.RESET, Часть3.connector8
  N2: Часть2.GND, Часть3.connector12
  N3: Часть2.D11/MOSI, Часть3.connector5
  N4: Часть2.3V3, Часть3.connector10
  N5: Часть2.D13/SCK, Часть3.connector6
  N6: R1.pin_0, R2.Pin_0
