# Fritzing sketch id2756_Rover_demo_0 (saved by Fritzing 0.9.3b)
breadboards: 1

parts:
  Part2 = Arduino Nano (Rev3.0) (ICSP)
  SW1 = DIP Switch 8 Position [package=dipswitch-08]
  Part3 = NRF24L01+ Breakout Board
  U1 = 74HC595 [package="DIP16 [THT]"]
  7_Segment1 = 7 Segment Display
  J1 = Basic Servo
  J2 = Basic Servo
  R1 = Resistor [tolerance=±5% resistance=330 package="2010 [SMD]"]
  R2 = Resistor [tolerance=±5% resistance=330 package="2010 [SMD]"]
  R3 = Resistor [tolerance=±5% resistance=330 package="2010 [SMD]"]
  R4 = Resistor [tolerance=±5% resistance=330 package="2010 [SMD]"]
  R5 = Resistor [tolerance=±5% resistance=330 package="2010 [SMD]"]
  R6 = Resistor [tolerance=±5% resistance=330 package="2010 [SMD]"]
  R7 = Resistor [tolerance=±5% resistance=330 package="2010 [SMD]"]
  R8 = Resistor [tolerance=±5% resistance=330 package="2010 [SMD]"]
  VCC1 = Battery
  VCC2 = Battery
  R9 = Resistor [tolerance=±5% resistance=4.7k package="2010 [SMD]"]
  R10 = Resistor [tolerance=±5% resistance=4.7k package="2010 [SMD]"]
  R11 = Resistor [tolerance=±5% resistance=4.7k package="2010 [SMD]"]
  R12 = Resistor [tolerance=±5% resistance=4.7k package="2010 [SMD]"]

nets:
  GND: Part2.GND, Part3.GND, U1.GND, J1.gnd, J2.gnd, VCC1.-, R9.Pin_1, R10.Pin_1, R11.Pin_1, R12.Pin_1
  N1: Part2.D2, U1.SH_CP
  N2: Part2.D3, U1.DS
  N3: Part2.D4, U1.OE
  N4: Part2.D5, J1.pulse
  N5: Part2.D6, J2.pulse
  N6: Part2.D7, SW1.16, R9.Pin_0
  N7: Part2.D8, SW1.15, R11.Pin_0
  N8: Part2.D9, SW1.14, R10.Pin_0
  N9: Part2.D10, SW1.13, R12.Pin_0
  N10: Part2.D11/MOSI, Part3.MOSI
  N11: Part2.D12/MISO, Part3.MISO
  VCC: Part2.VIN, J1.vcc, J2.vcc, VCC2.+
  5V: Part2.5V, U1.VCC, 7_Segment1.common_anode#3, 7_Segment1.common_anode#5, 7_Segment1.common_anode#11, 7_Segment1.common_anode#16
  N12: Part2.A3, Part3.CS
  N13: Part2.A2, Part3.CE
  3V3: Part2.3V3, SW1.1, SW1.2, SW1.3, SW1.4, Part3.VCC
  N14: Part2.D13/SCK, Part3.SCK
  N15: U1.Q1, R7.Pin_0
  N16: U1.Q2, R6.Pin_0
  N17: U1.Q3, R5.Pin_0
  N18: U1.Q4, R4.Pin_0
  N19: U1.Q5, R3.Pin_0
  N20: U1.Q6, R2.Pin_0
  N21: U1.Q7, R1.Pin_0
  N22: U1.Q0, R8.Pin_0
  N23: 7_Segment1.Segment_A, R8.Pin_1
  N24: 7_Segment1.Segment_F, R3.Pin_1
  N25: 7_Segment1.Segment_E, R4.Pin_1
  N26: 7_Segment1.Segment_DP, R1.Pin_1
  N27: 7_Segment1.Segment_D, R5.Pin_1
  N28: 7_Segment1.common_anode#12, R6.Pin_1
  N29: 7_Segment1.Segment_G, R2.Pin_1
  N30: 7_Segment1.Segment_B, R7.Pin_1
  N31: VCC1.+, VCC2.-
