# Fritzing sketch id2759_NanoCNC_1_2_0 (saved by Fritzing 0.9.3b)
circuit board: 9.90207cm x 10.3834cm
breadboards: 2

parts:
  Часть1 = Arduino Nano (Rev3.0)
  Pololu_A1 = Pololu A4988 [package=SO16]
  Pololu_A2 = Pololu A4988 [package=SO16]
  Pololu_A3 = Pololu A4988 [package=SO16]
  C1 = Electrolytic Capacitor [capacitance=1µF package="100 mil [THT, electrolytic]"]
  C2 = Electrolytic Capacitor [capacitance=1µF package="100 mil [THT, electrolytic]"]
  C3 = Electrolytic Capacitor [capacitance=1µF package="100 mil [THT, electrolytic]"]
  M1 = Stepper Motor - Bipolar
  M2 = Stepper Motor - Bipolar
  M3 = Stepper Motor - Bipolar
  J1 = Screw terminal - 2 pins [package=THT]
  R1 = Resistor [tolerance=±5% resistance=1k package=THT]

nets:
  N1: Часть1.GND, Pololu_A1.GND#8, Pololu_A2.GND#8, Pololu_A3.GND#8, R1.Pin_1
  N2: Часть1.D2, Pololu_A3.DIR
  N3: Часть1.D3, Pololu_A2.DIR
  N4: Часть1.D4, Pololu_A1.DIR
  N5: Часть1.D5, Pololu_A3.STEP
  N6: Часть1.D6, Pololu_A2.STEP
  N7: Часть1.D7, Pololu_A1.STEP
  VDD: Часть1.5V, Pololu_A1.VDD, Pololu_A2.VDD, Pololu_A3.VDD
  N8: Pololu_A1.RESET, Pololu_A1.SLEEP
  N9: Pololu_A1.1B, M3.D
  N10: Pololu_A1.1A, M3.B
  N11: Pololu_A1.2A, M3.C
  N12: Pololu_A1.2B, M3.A
  N13: Pololu_A1.GND#14, Pololu_A2.GND#14, Pololu_A3.GND#14, C1.-, C2.-, C3.-, J1.pin1
  N14: Pololu_A1.VMOT, Pololu_A2.VMOT, Pololu_A3.VMOT, C1.+, C2.+, C3.+, J1.pin2
  N15: Pololu_A2.RESET, Pololu_A2.SLEEP
  N16: Pololu_A2.1B, M2.D
  N17: Pololu_A2.1A, M2.B
  N18: Pololu_A2.2A, M2.C
  N19: Pololu_A2.2B, M2.A
  N20: Pololu_A3.RESET, Pololu_A3.SLEEP
  N21: Pololu_A3.1B, M1.D
  N22: Pololu_A3.1A, M1.B
  N23: Pololu_A3.2A, M1.C
  N24: Pololu_A3.2B, M1.A

notes:
  2
  1
  3
  V5+
  Grnd
  Dir
  Stp
  EndP
  D2
  D5
  D8
  D9
  D3
  D6
  D10
  D4
  D7
  Grnd.
  R
  Shymchenko
  Alexandr
  Garage HUB CNC
  2017
  "Vilka"
