# Fritzing sketch id275_bomb2.0_0 (saved by Fritzing 0.9.3b)
circuit board: 7.62933cm x 5.78833cm
breadboards: 1

parts:
  GREENLED = LED - 5mm [color="Green (570nm)" package="5 mm [THT]"]
  REDLED = LED - 5mm [color="Red (633nm)" package="5 mm [THT]"]
  SPKR1 = Loudspeaker
  R7 = Resistor [tolerance=±5% resistance=220 package=THT]
  R8 = Resistor [tolerance=±5% resistance=220 package=THT]
  Mosfet_Connection = screw terminal, 3 pins
  D_Button = Pushbutton [package="[THT]"]
  C_Button = Pushbutton [package="[THT]"]
  KEYBOARD = Generic male header - 8 pins [package=THT]
  R1 = Rotary Potentiometer (Small) [maximum_resistance=10kΩ package=THT]
  Arduino1 = Arduino Uno (Rev3)
  LCD1 = LCD screen

nets:
  GND: GREENLED.cathode, REDLED.cathode, SPKR1.pin2, Mosfet_Connection.pin1, R1.leg2, LCD1.VSS, LCD1.R/W, LCD1.LED-
  N1: GREENLED.anode, R8.Pin_1
  N2: REDLED.anode, R7.Pin_1
  N3: SPKR1.pin1, Arduino1.D8
  5V: Mosfet_Connection.pin2, R1.leg1, LCD1.VDD, LCD1.LED+
  N4: D_Button.Pin_1, D_Button.Pin_2, KEYBOARD.pin7
  N5: D_Button.Pin_3, D_Button.Pin_4, C_Button.Pin_3, C_Button.Pin_4, KEYBOARD.pin4, Arduino1.A3
  N6: C_Button.Pin_2, KEYBOARD.pin8
  N7: KEYBOARD.pin1, Arduino1.A0
  N8: KEYBOARD.pin2, Arduino1.A1
  N9: KEYBOARD.pin3, Arduino1.A2
  N10: R1.wiper, LCD1.V0
  N11: Arduino1.D2, LCD1.DB7
  N12: Arduino1.D4, LCD1.DB5
  N13: Arduino1.D7, LCD1.RS

notes:
  keyboard matrix 4x4
  'C' or Left button Connected to pin 4 & 7
  'D' or Right button
  Conected to pin 4 & 8
