# Fritzing sketch id2762_NanoCNC_2_1_0 (saved by Fritzing 0.9.3b)
circuit board: 9.90207cm x 10.3834cm
breadboards: 2

parts:
  Часть1 = Arduino Nano (Rev3.0)
  C1 = Electrolytic Capacitor [capacitance=1µF package="100 mil [THT, electrolytic]"]
  C2 = Electrolytic Capacitor [capacitance=1µF package="100 mil [THT, electrolytic]"]
  C3 = Electrolytic Capacitor [capacitance=1µF package="100 mil [THT, electrolytic]"]
  M1 = Stepper Motor - Bipolar
  M2 = Stepper Motor - Bipolar
  M3 = Stepper Motor - Bipolar
  J1 = Screw terminal - 2 pins [package=THT]
  R1 = Resistor [tolerance=±5% resistance=1k package=THT]
  Pololu_A1 = Pololu A4988 [package=SO16]
  Pololu_A2 = Pololu A4988 [package=SO16]
  Pololu_A3 = Pololu A4988 [package=SO16]

nets:
  N1: Часть1.GND, R1.Pin_1, Pololu_A2.GND#8, Pololu_A3.GND#8
  N2: Часть1.D2, Pololu_A1.STEP
  N3: Часть1.D3, Pololu_A2.STEP
  N4: Часть1.D4, Pololu_A3.STEP
  N5: Часть1.D5, Pololu_A1.DIR
  N6: Часть1.D6, Pololu_A2.DIR
  N7: Часть1.D7, Pololu_A3.DIR
  VDD: Часть1.5V, Pololu_A1.VDD, Pololu_A2.VDD, Pololu_A3.VDD
  N8: C1.-, C2.-, C3.-, J1.pin1, Pololu_A1.GND#14, Pololu_A2.GND#14, Pololu_A3.GND#14
  N9: C1.+, C2.+, C3.+, J1.pin2, Pololu_A1.VMOT, Pololu_A2.VMOT, Pololu_A3.VMOT
  N10: M1.A, Pololu_A1.2B
  N11: M1.C, Pololu_A1.2A
  N12: M1.B, Pololu_A1.1A
  N13: M1.D, Pololu_A1.1B
  N14: M2.A, Pololu_A2.2B
  N15: M2.C, Pololu_A2.2A
  N16: M2.B, Pololu_A2.1A
  N17: M2.D, Pololu_A2.1B
  N18: M3.A, Pololu_A3.2B
  N19: M3.C, Pololu_A3.2A
  N20: M3.B, Pololu_A3.1A
  N21: M3.D, Pololu_A3.1B
  N22: Pololu_A1.RESET, Pololu_A1.SLEEP
  N23: Pololu_A2.RESET, Pololu_A2.SLEEP
  N24: Pololu_A3.RESET, Pololu_A3.SLEEP

notes:
  V5+
  Grnd
  R
  CNC
  HUB
  Garage
  2017
  X
  Y
  Z
  G
  5+
