# Fritzing sketch id2765_NAS_Ethernet_Switch_0 (saved by Fritzing 0.9.2b)

parts:
  ENC28J1 = ENC28J69
  KY-1 = keyes
  Part2 = Arduino Pro Mini v13
  U1 = V_REG_LD1117VXX [package=78xxl]
  R1 = Resistor [tolerance=±5% resistance=1k package=THT]
  R2 = Resistor [tolerance=±5% resistance=1k package=THT]
  LED1 = LED - 3mm [color="Green (555nm)" package="3 mm [THT]"]
  J1 = Power Jack [package=power_jack_slot]
  J2 = COMPUTER-PERIPHERAL-POWER [package=computer-peripheral-power-ra]

nets:
  N1: ENC28J1.connector2, Part2.D12/MISO
  N2: ENC28J1.connector3, Part2.D13/SCK
  N3: ENC28J1.connector6, U1.OUT
  N4: ENC28J1.connector10, Part2.D11_PWM/MOSI
  N5: ENC28J1.connector11, Part2.D10_PWM/SS
  N6: KY-1.connector0, Part2.D7
  GND: Part2.GND, J1.GND
  N7: Part2.VCC, J1.GNDBREAK
  N8: Part2.A1, R1.Pin_1, R2.Pin_0, LED1.anode
  N9: R1.Pin_0, LED1.cathode, J2.GND
  N10: R2.Pin_1, J2.5V
