# Fritzing sketch id2767_Fritzing_Spaceship_Interface_Project_0 (saved by Fritzing 0.7.5b)
breadboards: 1

parts:
  LED1 = LED - 5mm [color="Red (633nm)" package="5 mm [THT]"]
  LED2 = LED - 5mm [color="Red (633nm)" package="5 mm [THT]"]
  LED3 = LED - 5mm [color="Red (633nm)" package="5 mm [THT]"]
  R1 = Resistor [tolerance=±5% resistance=220 package=THT]
  R2 = Resistor [tolerance=±5% resistance=220 package=THT]
  R3 = Resistor [tolerance=±5% resistance=220 package=THT]
  S1 = Pushbutton [package="[THT]"]
  R4 = Resistor [tolerance=±5% resistance=220 package=THT]
  Arduino1 = Arduino  # not connected

nets:
  N1: LED1.anode, R1.Pin_1
  N2: LED2.anode, R2.Pin_1
  N3: LED3.anode, R3.Pin_1
  N4: R1.Pin_0, R2.Pin_0, R3.Pin_0, R4.Pin_0
  N5: S1.Pin_1, S1.Pin_2, R4.Pin_1
  N6: S1.Pin_3, S1.Pin_4
