# Fritzing sketch id2768_PCB_NANO_0 (saved by Fritzing 0.9.3b)
circuit board: 5.11458cm x 5.90705cm
breadboards: 1

parts:
  Part1 = Arduino Nano (Rev3.0)
  U1 = RF-LINK_TX [package=rf-link_tx]
  U2 = RF-LINK_TX [package=rf-link_tx]
  J1 = Screw terminal - 2 pins [package=THT]
  J2 = Screw terminal - 2 pins [package=THT]
  J3 = Screw terminal - 2 pins [package=THT]
  J4 = Screw terminal - 2 pins [package=THT]
  J5 = Screw terminal - 2 pins [package=THT]
  J6 = Screw terminal - 2 pins [package=THT]
  Part2 = Arduino Nano (Rev3.0)  # not connected

nets:
  GND: Part1.GND, U1.GND, U2.GND, J5.pin1, J6.pin1
  N1: Part1.D2, J6.pin2
  N2: Part1.D3, J5.pin2
  N3: Part1.D4, U2.DATA
  N4: Part1.D5, U1.DATA
  N5: Part1.D12/MISO, J4.pin2
  5V: Part1.5V, U1.+5V, J1.pin1, J2.pin2, J3.pin2
  N6: Part1.A7, J1.pin2
  N7: Part1.A5, J2.pin1
  N8: Part1.A1, J3.pin1
  N9: U2.+5V, J4.pin1
