# Fritzing sketch id2769_probador_ne555_0 (saved by Fritzing 0.9.2b)
breadboards: 1

parts:
  U1 = 555 Timer [package="DIP8 [THT]"]
  R1 = Resistor [tolerance=±5% resistance=220 package=THT]
  C1 = Ceramic Capacitor [capacitance=100nF package="100 mil [THT, multilayer]"]
  C2 = Electrolytic Capacitor [capacitance=1µF package="100 mil [THT, electrolytic]"]
  R2 = Resistor [tolerance=±5% resistance=6.8k package=THT]
  R3 = Resistor [tolerance=±5% resistance=10.k package=THT]
  LED1 = LED - 5mm [color="Red (633nm)" package="5 mm [THT]"]  # not connected

nets:
  N1: U1.Ground, C1.1, C2.-
  N2: U1.Trigger, U1.Threshold, C2.+, R3.Pin_1
  N3: U1.Output, R1.Pin_0
  N4: U1.Control_Voltage, C1.0
  N5: U1.Discharge, R2.Pin_0, R3.Pin_0
  N6: U1.Vcc_Supply_Voltage, R2.Pin_1
