# Fritzing sketch id276_arduino_timer_bomb_airsoft_0 (saved by Fritzing 0.7.1b)

parts:
  LCD1 = LCD screen
  SPKR1 = Loudspeaker
  R1 = Rotary Potentiometer (Small) [maximum_resistance=100kΩ]
  LED1 = LED - 5mm [color="Red (633nm)" package="5 mm [THT]"]
  LED2 = LED - 5mm [color="Green (570nm)" package="5 mm [THT]"]
  Arduino1 = Arduino
  R3 = Resistor [tolerance=±20% resistance=1k package=THT]
  R2 = Resistor [tolerance=±20% resistance=1k package=THT]
  R1_2 = Resistor [tolerance=±20% resistance=1k package=THT]
  R4 = Resistor [tolerance=±20% resistance=1k power=5W package=THT]

nets:
  VSS: LCD1.VSS, LCD1.DB5, LCD1.LED-, SPKR1.pin1, R1.leg2, LED1.cathode, LED2.cathode, Arduino1.GND
  VDD: LCD1.VDD, LCD1.LED+, R1.leg1, Arduino1.+5V
  N1: LCD1.V0, Arduino1.D13
  N2: LCD1.RS, Arduino1.D12
  N3: LCD1.R/W, Arduino1.D11
  N4: LCD1.E, Arduino1.D10
  N5: LCD1.DB4, Arduino1.D8
  N6: LCD1.DB6, Arduino1.D7
  N7: LCD1.DB7, R1.wiper
  N8: SPKR1.pin2, Arduino1.D9
  N9: LED1.anode, Arduino1.D3
  N10: LED2.anode, Arduino1.D4
  N11: Arduino1.A1, R1_2.Pin_1
  N12: Arduino1.A3, R2.Pin_1
  N13: Arduino1.A4, R3.Pin_1
  N14: Arduino1.A5, R4.Pin_1

notes:
  Airsoft , Aduino Shield Timer Bomb, rev 1
  Arduino Timer Bomb
  A5     A4    A3 A2 A1 A0
  VIN GND GND 5V 3.3V RST
  Red and green LED
  Made by AAG
