# Fritzing sketch id2770_GY_NEO6MV2_0 (saved by Fritzing 0.9.2b)
breadboards: 1

parts:
  Bauteil1 = Arduino Uno (Rev3)
  R1 = Resistor [tolerance=±5% resistance=4.7k package="1206 [SMD]"]
  R2 = Resistor [tolerance=±5% resistance=10k package="1206 [SMD]"]
  GY-NEO6MV2 = SUP500F [package=sup500f]

nets:
  N1: Bauteil1.D3_PWM, GY-NEO6MV2.VCC
  N2: Bauteil1.D4, R1.Pin_0
  N3: Bauteil1.5V, GY-NEO6MV2.TX-O
  N4: Bauteil1.GND, R2.Pin_1, GY-NEO6MV2.RX-I
  N5: R1.Pin_1, R2.Pin_0, GY-NEO6MV2.GND

notes:
  GND: Black
  VCC: Red
  RX: Yellow
  TX: Green
