# Fritzing sketch id2772_Neopixel_0 (saved by Fritzing 0.9.3b)

parts:
  Part1 = Arduino Uno (Rev3)
  J1 = JST-VHR-3N [part_number=JST-VHR-3N package=THT]

nets:
  N1: Part1.GND, J1.pin_6
  N2: Part1.VIN, J1.pin_4
