# Fritzing sketch id2773_neoPixelDriverV1_0 (saved by Fritzing 0.9.1b)
circuit board: 2.48737cm x 3.63008cm
breadboards: 1

parts:
  Pad1 = Pad [width=2 height=6 connect=center]
  Pad2 = Pad [width=2 height=6 connect=center]
  Pad3 = Pad [width=2 height=6 connect=center]
  Pad4 = Pad [width=2 height=6 connect=center]
  Pad5 = Pad [width=2 height=6 connect=center]  # not connected
  Pad6 = Pad [width=2 height=6 connect=center]
  Pad7 = Pad [width=2 height=6 connect=center]  # not connected
  Pad8 = Pad [width=2 height=6 connect=center]  # not connected
  vReg = Voltage Regulator - 5V [package="DPak [SMD]"]
  1uf = Electrolytic Capacitor [capacitance=1µF package="0405 [SMD, electrolytic]"]
  10uf = Electrolytic Capacitor [capacitance=1µF package="0405 [SMD, electrolytic]"]
  +_- = Battery
  switch = female pin header, 2 pins [form="♀ (female)"]
  -_0_1_+ = female pin header, 4 pins [form="♀ (female)"]
  sensor = Basic Force Sensing Resistor (FSR) [package=THT]
  R1 = Resistor [tolerance=±5% resistance=220 package="1206 [SMD]"]

nets:
  N1: Pad1.pad, vReg.input_voltage, 1uf.+, -_0_1_+.pin1
  N2: Pad2.pad, sensor.pin_0, R1.Pin_0
  N3: Pad3.pad, -_0_1_+.pin2, sensor.pin_1
  N4: Pad4.pad, -_0_1_+.pin3
  N5: Pad6.pad, vReg.GND, 1uf.-, 10uf.-, +_-.-, -_0_1_+.pin4, R1.Pin_1
  N6: vReg.output_voltage, 10uf.+, switch.pin2
  N7: +_-.+, switch.pin1

notes:
  (-)
  (+)
  rst
  a3
  a2
  gnd
  a1
  d0
  vcc
  d1
  []
