# Fritzing sketch id2774_neopixel_strip_example_0 (saved by Fritzing 0.9.2b)
breadboards: 1

parts:
  C1 = Electrolytic Capacitor [capacitance=1mF package="0807 [SMD, electrolytic]"]
  부품1 = Breadboard Power Supply Board SMD  # not connected
  R1 = Resistor [tolerance=±5% resistance=330 package=THT]
  부품2 = Arduino Uno (Rev3)
  NEOPIXEL1 = Neopixel_Strip____Black__30_m

nets:
  N1: C1.-, 부품2.GND, NEOPIXEL1.connector3
  N2: C1.+, NEOPIXEL1.connector1
  N3: R1.Pin_0, NEOPIXEL1.connector2
  N4: R1.Pin_1, 부품2.D6_PWM
