# Fritzing sketch id2776_spark_neopixel_basic_0 (saved by Fritzing 0.9.0b)
breadboards: 1

parts:
  Part1 = Spark Core (v1.0)
  R1 = Resistor [tolerance=±5% resistance=220 package=THT]
  NEOPIXEL1 = Neopixel_Strip____White__60_m

nets:
  N1: Part1.GND, NEOPIXEL1.connector3
  N2: Part1.VIN, NEOPIXEL1.connector2
  N3: Part1.D2, R1.Pin_1
  N4: R1.Pin_0, NEOPIXEL1.connector1
