# Fritzing sketch id2777_Auto_Nerf_Turret_0 (saved by Fritzing 0.7.4b)
breadboards: 2

parts:
  Arduino1 = Arduino
  J1 = Infrared Proximity Sensor
  C1 = Electrolytic Capacitor [capacitance=10µF package="100 mil [THT, electrolytic]"]
  SPKR1 = Loudspeaker  # not connected
  VCC1 = Battery  # not connected
  K1 = Relay [part_number=FRS1B-S package=THT]
  D1 = Rectifier Diode [part_number=1N4001 package="300 mil [THT]"]
  Part1 = Triple Axis Accelerometer Breakout - ADXL335

nets:
  GND: Arduino1.GND, J1.GND, C1.-, K1.A, Part1.GND
  N1: Arduino1.D8, K1.B, D1.cathode
  3V3: Arduino1.3V3, Part1.VCC
  +5V: Arduino1.+5V, J1.Vcc, C1.+
  N2: Arduino1.A0, Part1.XOUT
  N3: Arduino1.A1, Part1.YOUT
  N4: Arduino1.A2, Part1.ZOUT
  N5: Arduino1.A5, J1.Vout
  N6: K1.C1, K1.C2

notes:
  Nerf firing mechanisim
  Whatever makes sound will go over here.
  Prolly shitty mp3 controled from relay.
  Look more into it later.
  LED array ova here.
