# Fritzing sketch id2778_nerf_upgrade_0 (saved by Fritzing 0.7.5b)
breadboards: 1

parts:
  LED1 = LED - 5mm [color="Red (633nm)" package="5 mm [THT]"]
  LED2 = LED - 5mm [color="Red (633nm)" package="5 mm [THT]"]
  LED3 = LED - 5mm [color="Red (633nm)" package="5 mm [THT]"]
  LED4 = LED - 5mm [color="Red (633nm)" package="5 mm [THT]"]
  LED5 = LED - 5mm [color="Red (633nm)" package="5 mm [THT]"]
  LED6 = LED - 5mm [color="Red (633nm)" package="5 mm [THT]"]
  R1 = Resistor [tolerance=±5% resistance=220 package=THT]
  R3 = Resistor [tolerance=±5% resistance=220 package=THT]
  R4 = Resistor [tolerance=±5% resistance=220 package=THT]
  R5 = Resistor [tolerance=±5% resistance=220 package=THT]
  R6 = Resistor [tolerance=±5% resistance=220 package=THT]
  R7 = Resistor [tolerance=±5% resistance=220 package=THT]
  IR_Receiver = mystery part, 3 pins [chip_label=? spacing=300mil]
  IR_LED = LED - 5mm [color="Red (633nm)" package="5 mm [THT]"]
  R8 = Resistor [tolerance=±5% resistance=100 package=THT]
  R9 = Resistor [tolerance=±5% resistance=100 package=THT]
  S3 = Pushbutton [package=THT]
  S4 = Toggle Switch [package=THT]
  Teensy1 = Teensy 2.0
  3_7V_LiPo_battery = Battery

nets:
  N1: LED1.cathode, LED2.cathode, LED3.cathode, LED4.cathode, LED5.cathode, LED6.cathode, IR_Receiver.pin2, IR_LED.cathode, 3_7V_LiPo_battery.-
  N2: LED1.anode, R1.Pin_0
  N3: LED2.anode, R7.Pin_0
  N4: LED3.anode, R6.Pin_0
  N5: LED4.anode, R5.Pin_0
  N6: LED5.anode, R4.Pin_0
  N7: LED6.anode, R3.Pin_0
  N8: R1.Pin_1, Teensy1.F6
  N9: R3.Pin_1, Teensy1.D7
  N10: R4.Pin_1, Teensy1.B4
  N11: R5.Pin_1, Teensy1.B5
  N12: R6.Pin_1, Teensy1.B6
  N13: R7.Pin_1, Teensy1.F7
  N14: IR_Receiver.pin1, Teensy1.D4
  N15: IR_Receiver.pin3, R8.Pin_0
  N16: IR_LED.anode, R9.Pin_0
  N17: R8.Pin_1, Teensy1.F5
  N18: R9.Pin_1, Teensy1.F4
  N19: S3.leg0, Teensy1.GND
  N20: S3.leg1, Teensy1.RST
  N21: S4.L2, 3_7V_LiPo_battery.+

notes:
  reset pushbutton
  NERF MAVERICK UPGRADE - build 110812 - nimrod316@gmx.de
  - the 6 LEDs represent the bullets in the barrel.
  - the IR LED and the IR Receiver are placed inside the bullet runway facing each other. Thus whenever a foam arrow interrupts the visual connection between Emitter and Receiver a shot was fired.
  - the single grey wire is actually attached to the trigger. deisolate its plastic. same for the wire that goes into GND. the human hand touches both wires for best capacitive results. inside the code, if you do not touch the wire attached to the trigger and the pin, no diods are HIGH => saves battery power. the shot-counter only triggers as well, if you touch the trigger wire, which actually makes sense.
  - place the reset switch in an appropriate spot inside the gun. possibly where it automatically triggers whenever you reload the barrel.
  changes:
  - thanks to paul from prjc.com (makers of teensy) for updating the arduino capacitive code. no need for the capsense lib anymore.
  notes:
  - to apply external power to the teensy, cut the power lines on its bottom side, see the manual for more information.
  bugs:
  Cap wire between GND and hand
  Cap between Pin and trigger
