# Fritzing sketch id2779_Microsoft_.NET_Gadgeteer_Serial_Interface_Module_0 (saved by Fritzing 0.7.5b)
breadboards: 1

parts:
  Part3 = FTDI Basic Programmer
  J1 = shrouded pin header, 10 pins [form="♂ (shrouded male)"]

nets:
  N1: Part3.DTR, J1.pin6
  N2: Part3.RXI, J1.pin5
  N3: Part3.TXO, J1.pin4
  N4: Part3.POWER, J1.pin1
  N5: Part3.CTS, J1.pin7
  N6: Part3.GND, J1.pin10

notes:
  .NET Gadgeteer Serial Interface Board
