# Fritzing sketch id277_Bahce_Sulama_0 (saved by Fritzing 0.9.3b)
breadboards: 1

parts:
  Parça1 = Arduino Uno (Rev3)  # not connected
  LCD1 = LCD screen
  Nem_3 = Soil Moisture Sensor  # not connected
  Nem_2 = Soil Moisture Sensor  # not connected
  Nem_1 = Soil Moisture Sensor  # not connected
  Nem_4 = Soil Moisture Sensor  # not connected
  Röle_3 = RELAY [package=relay-jzc]
  Röle_2 = RELAY [package=relay-jzc]
  Röle_1 = RELAY [package=relay-jzc]
  Röle_4 = RELAY [package=relay-jzc]
  Vana_4 = Solenoid
  Vana_3 = Solenoid
  Vana_2 = Solenoid
  Vana_1 = Solenoid
  R1 = Resistor [tolerance=±5% resistance=100 package=THT]
  R2 = Resistor [tolerance=±5% resistance=220 package=THT]

nets:
  N1: LCD1.V0, R1.Pin_0
  N2: LCD1.LED+, R2.Pin_0
  N3: Röle_3.MAIN, Vana_3.pin2
  N4: Röle_3.COIL1, Vana_3.pin1
  N5: Röle_2.MAIN, Vana_2.pin2
  N6: Röle_2.COIL1, Vana_2.pin1
  N7: Röle_1.MAIN, Vana_1.pin2
  N8: Röle_1.COIL1, Vana_1.pin1
  N9: Röle_4.MAIN, Vana_4.pin2
  N10: Röle_4.COIL1, Vana_4.pin1
