# Fritzing sketch id2780_MyFirstRobot_0 (saved by Fritzing 0.8.5b)
breadboards: 1

parts:
  Netduino_1 = Netduino2
  IC1 = L293D [package=THT]
  BAT1 = BC9VPC [package=bc9vpc]
  M1 = DC Motor
  M2 = DC Motor
  Εξάρτημα2 = SRF05 Ultrasonic Rangefinder

nets:
  N1: Netduino_1.connector4, Εξάρτημα2.connector10
  N2: Netduino_1.connector5, IC1.Enable_2
  N3: Netduino_1.connector6, IC1.Enable_1
  N4: Netduino_1.connector7, Εξάρτημα2.connector9
  N5: Netduino_1.connector12, IC1.In_4
  N6: Netduino_1.connector13, IC1.In_3
  N7: Netduino_1.connector14, IC1.In_2
  N8: Netduino_1.connector15, IC1.In_1
  N9: Netduino_1.connector18, IC1.+V, Εξάρτημα2.connector8
  N10: Netduino_1.connector20, IC1.0V, BAT1.V+, Εξάρτημα2.connector11
  N11: Netduino_1.connector21, IC1.+Vmotor, BAT1.V-
  N12: IC1.Out_1_(_Controlled_by_Enable_1_), M2.pin_2
  N13: IC1.Out_2_(_Controlled_by_Enable_1_), M2.pin_1
  N14: IC1.Out_3_(_Controlled_by_Enable_2_), M1.pin_2
  N15: IC1.Out_4_(_Controlled_by_Enable_2_), M1.pin_1
