# Fritzing sketch id2781_ar_0 (saved by Fritzing 0.9.3b)
stripboards: 1

parts:
  D1 = Rectifier Diode [part_number=1N4001 package="300 mil [THT]"]
  Q1 = NPN-Transistor [package="TO92 [THT]"]
  Q2 = NPN-Transistor [package="TO92 [THT]"]
  R1 = Resistor [tolerance=±5% resistance=2k package=THT]
  R2 = Resistor [tolerance=±5% resistance=2k package=THT]
  D2 = Rectifier Diode [part_number=1N4001 package="300 mil [THT]"]
  Part2 = Arduino XBee Shield
  L1 = Solenoid
  L2 = Solenoid
  R3 = Resistor [tolerance=±5% resistance=10k package=THT]
  R4 = Resistor [tolerance=±5% resistance=10k package=THT]
  R5 = Resistor [tolerance=±5% resistance=10k package=THT]
  VCC1 = 4 x AAA Battery Mount
  J1 = Basic Force Sensing Resistor (FSR) [package=THT]
  J2 = Basic Force Sensing Resistor (FSR) [package=THT]
  J3 = Basic Force Sensing Resistor (FSR) [package=THT]
  J4 = Infrared Proximity Sensor
  U1 = VCNL4000 [package=vcnl4000]

nets:
  N1: D1.cathode, D2.cathode, Part2.N$82, Part2.N$83, Part2.N$84, L1.pin2, L2.pin2, VCC1.+
  N2: D1.anode, Q1.C, Part2.N$128, Part2.N$129, Part2.N$130, L2.pin1
  N3: Q1.E, Q2.E, Part2.N$95, Part2.N$105, Part2.N$109, VCC1.-
  N4: Q1.B, R1.Pin_0, Part2.N$116, Part2.N$117
  N5: Q2.B, R2.Pin_0, Part2.N$121, Part2.N$122
  N6: Q2.C, D2.anode, Part2.N$132, Part2.N$133, Part2.N$134, L1.pin1
  N7: R1.Pin_1, Part2.D13, Part2.N$56, Part2.N$68
  N8: R2.Pin_1, Part2.D12, Part2.N$62, Part2.N$74
  GND: Part2.GND, Part2.N$23, Part2.N$34, Part2.N$35, Part2.N$48, Part2.N$100, Part2.N$101, R3.Pin_1, R4.Pin_1, R5.Pin_1, J4.GND, U1.GND
  5V: Part2.5V, Part2.N$112, Part2.N$113, J1.pin_1, J2.pin_1, J3.pin_1, J4.Vcc, U1.VDD
  N9: Part2.A0, Part2.N$65, Part2.N$66, J4.Vout
  N10: Part2.A1, Part2.N$52, Part2.N$53, Part2.N$54, R5.Pin_0, J1.pin_0
  N11: Part2.A2, Part2.N$40, Part2.N$41, Part2.N$42, R4.Pin_0, J2.pin_0
  N12: Part2.A3, Part2.N$27, Part2.N$28, Part2.N$29, R3.Pin_0, J3.pin_0
  N13: Part2.D10, Part2.N$31, Part2.N$32, Part2.N$76, Part2.N$77, U1.SDA
  N14: Part2.D11, Part2.N$44, Part2.N$45, Part2.N$88, Part2.N$89, U1.SCL
