# Fritzing sketch id2782_New_GoGo_Display_0 (saved by Fritzing 0.9.2b)
breadboards: 1

parts:
  U1 = PCF8574 [package="DIP16 [THT]"]
  LCD1 = LCD screen
  J1 = screw terminal, 3 pins
  J2 = screw terminal, 3 pins
  R1 = Trimmer Potentiometer [maximum_resistance=10kΩ package=THT]

nets:
  N1: U1.A0, U1.A1, U1.A3, R1.leg2
  N2: U1.P0, LCD1.DB4
  N3: U1.P1, LCD1.DB5
  N4: U1.P2, LCD1.DB6
  N5: U1.P3, LCD1.DB7
  GND: U1.GND, LCD1.VSS, LCD1.LED-, J1.pin3, R1.leg1
  N6: U1.P4, LCD1.RS
  N7: U1.P5, LCD1.R/W
  N8: U1.P6, LCD1.E
  N9: U1.SCL, J1.pin2
  N10: U1.SDA, J1.pin1
  VCC: U1.VCC, LCD1.VDD, LCD1.LED+, J2.pin3
  N11: LCD1.V0, R1.wiper

notes:
  Br-GoGo I2C
