# Fritzing sketch id2783_NexaAutoControl_0 (saved by Fritzing 0.9.1b)
breadboards: 1

parts:
  Part1 = Arduino Uno (Rev3)  # not connected
  Part2 = Arduino Ethernet Shield (Rev3)
  R1 = Resistor [tolerance=±5% resistance=10k package=THT]
  R2 = Photocell (LDR) [package=THT]
  Part3 = Real Time Clock Module - DS1307 RTC Breakout Board [part_number=DS3231]
  U1 = RF-LINK_RX [part_number=MX-JS-05V package=rf-link_rx]
  U2 = RF-LINK_TX [part_number=XY-FST package=rf-link_tx]

nets:
  5V: Part2.5V, R2.pin_1, Part3.5V, U1.+5V, U2.+5V
  N1: Part2.D8, Part2.D2, U1.DATA
  N2: Part2.A0, R1.Pin_1, R2.pin_0
  N3: Part2.A4/SDA, Part3.SDA
  N4: Part2.A5/SCL, Part3.SCL
  N5: Part2.D7, U2.DATA
  GND: Part2.GND, R1.Pin_0, Part3.GND, U1.GND, U2.GND
