# Fritzing sketch id2785_nightlight_0 (saved by Fritzing 0.9.1b)
breadboards: 1

parts:
  Part1 = Arduino Uno (Rev3)
  R1 = PHOTOCELL [package=photocell]
  R2 = Resistor [package="2512 [SMD]"]
  R3 = Resistor [package="2512 [SMD]"]
  LED1 = LED - 5mm [color="Red (633nm)" package="5 mm [THT]"]

nets:
  N1: Part1.A0, R1.P$2, R2.Pin_1
  N2: Part1.D3_PWM, R3.Pin_0
  N3: Part1.5V, R1.P$1
  N4: Part1.GND, LED1.cathode
  N5: R2.Pin_0, R3.Pin_1, LED1.anode
