# Fritzing sketch id2786_FINAL_ARDUINO_PROJ_0 (saved by Fritzing 0.9.3b)
breadboards: 1

parts:
  Part1 = Arduino Pro
  R1 = Resistor [tolerance=±5% resistance=220 package="1206 [SMD]"]
  R2 = PHOTOCELL [package=photocell-kit]
  LED1 = LED - 5mm [color="Blue (470nm)" package="5 mm [THT]"]
  LED2 = LED - 5mm [color="Blue (470nm)" package="5 mm [THT]"]
  LED3 = LED - 5mm [color="Blue (470nm)" package="5 mm [THT]"]
  R3 = Resistor [tolerance=±5% resistance=220 package="0603 [SMD]"]
  R4 = Resistor [tolerance=±5% resistance=220 package="0603 [SMD]"]
  R5 = Resistor [tolerance=±5% resistance=220 package="0603 [SMD]"]
  LED4 = smd LED [color="Blue (470nm)" package="0805 [SMD]"]
  R6 = Resistor [tolerance=±5% resistance=220 package="0603 [SMD]"]
  LED5 = smd LED [color="Blue (470nm)" package="0805 [SMD]"]
  R7 = Resistor [tolerance=±5% resistance=220 package="0603 [SMD]"]
  LED6 = smd LED [color="Blue (470nm)" package="0805 [SMD]"]
  R8 = Resistor [tolerance=±5% resistance=220 package="0603 [SMD]"]
  LED7 = LED_RING [package=led_ring]

nets:
  N1: Part1.D2, LED4.anode, R6.Pin_1
  N2: Part1.D4/A6, R8.Pin_1
  N3: Part1.D6_PWM, Part1.GND, R1.Pin_1, LED1.cathode, LED2.cathode, LED3.cathode, LED4.cathode, LED5.cathode, LED6.cathode, LED7.5, LED7.7, LED7.8, LED7.9, LED7.10, LED7.12, LED7.13, LED7.14, LED7.15, LED7.16
  N4: Part1.D7, LED5.anode, R7.Pin_1
  N5: Part1.A0, R1.Pin_0, R2.P$2
  N6: Part1.D8, R3.Pin_1
  N7: Part1.D12/MISO, R5.Pin_1
  N8: Part1.D13/SCK, R4.Pin_1
  N9: Part1.3V3, R2.P$1, LED7.COM0
  N10: LED1.anode, R3.Pin_0
  N11: LED2.anode, R4.Pin_0
  N12: LED3.anode, R5.Pin_0
