# Fritzing sketch id2787_nightlight_0 (saved by Fritzing 0.9.3b)
circuit board: 8.46667cm x 5.64444cm
breadboards: 1

parts:
  Q2 = PNP-Transistor [package="TO92 [THT]"]
  LED1 = LED - 5mm [color="Red (633nm)" package="5 mm [THT]"]
  R1 = Resistor [tolerance=±5% resistance=4.7k package=THT]
  R2 = Photocell (LDR) [package=THT]
  BAT1 = Battery Holders [package=battcom_20mm_pth]

nets (from the schematic view):
  N1: Q2.E, LED1.cathode
  N2: Q2.B, R1.Pin_1, R2.pin_0
  N3: Q2.C, R1.Pin_0, BAT1.-
  N4: LED1.anode, R2.pin_1, BAT1.+
