# Fritzing sketch id2788_Niklas_RobotArm_0 (saved by Fritzing 0.9.3b)

parts:
  Poti = Rotary Potentiometer (Large) [maximum_resistance=10kΩ package=THT]
  ATmega328P = Arduino Uno (Rev3)
  Joystick = Thumb Joystick
  J2_Y-Achse = Basic Servo
  J3_Greifer = Basic Servo
  J1_X-Achse = Basic Servo

nets:
  GND: Poti.leg1, ATmega328P.GND, Joystick.GND, J2_Y-Achse.gnd, J3_Greifer.gnd, J1_X-Achse.gnd
  VCC: Poti.leg2, ATmega328P.5V, Joystick.VCC, J2_Y-Achse.vcc, J3_Greifer.vcc, J1_X-Achse.vcc
  N1: ATmega328P.A0, Joystick.HORZ
  N2: ATmega328P.A1, Joystick.VERT
  N3: ATmega328P.D9_PWM, J1_X-Achse.pulse
  N4: ATmega328P.D10_PWM/SS, J2_Y-Achse.pulse
  N5: ATmega328P.D11_PWM/MOSI, J3_Greifer.pulse
  N6: ATmega328P.D2, Joystick.SEL
