# Fritzing sketch id2789_custom_iScan_0 (saved by Fritzing 0.9.2b)

parts:
  부품1 = Arduino Uno (Rev3)
  U3 = LCD-16X2 [package=lcd-16x2_noholes]
  BAT1 = BC9VPC [package=bc9vpc]
  Part1 = Arduino ProtoShield
  S1 = Round Pushbutton
  J2 = Basic Force Sensing Resistor (FSR) [package=THT]
  R2 = Resistor [tolerance=±5% resistance=10k package=THT]
  J3 = Basic Force Sensing Resistor (FSR) [package=THT]
  R3 = Resistor [tolerance=±5% resistance=10k package=THT]

nets:
  GND: 부품1.GND, U3.VSS, BAT1.V-, Part1.GND, Part1.N$87, Part1.N$154, R2.Pin_1, R3.Pin_1
  5V: 부품1.5V, U3.VO, Part1.LED1, Part1.5V, S1.leg1, J2.pin_0, J3.pin_0
  N1: U3.R_W, Part1.TX
  N2: BAT1.V+, S1.leg0
  N3: Part1.A1, Part1.N$43, J3.pin_1, R3.Pin_0
  N4: Part1.A0, Part1.N$110, J2.pin_1, R2.Pin_0
