# Fritzing sketch id2790_esquema_robotica_0 (saved by Fritzing 0.9.3b)

parts:
  Raspberry_Pi1 = Raspberry Pi 2
  U1 = TRANSCHIPTC5747 [package=camera_sfv24r-2st_2]
  X2 = USB Connectors [package=usb-a-h]  # not connected
  BAT1 = Battery Holders [package=lipo-1100mAh]  # not connected
  U2 = RJ45 Jack [package=rj45-8]  # not connected
  D1 = SOLAR-IXYS [package=solarbit-12x1]  # not connected

nets:
  3V3: Raspberry_Pi1.3v3, Raspberry_Pi1.3V3, U1.VCLK_OUT, U1.LED_CTRL
  N1: Raspberry_Pi1.GPIO2, U1.SHIELD
  N2: Raspberry_Pi1.GPIO3, U1.PS2
  N3: Raspberry_Pi1.GPIO4, U1.PS1
  N4: Raspberry_Pi1.GND, U1.AVDD28, U1.DOUT_0, U1.DOUT_3, U1.SDIN
  N5: Raspberry_Pi1.GPIO17, U1.DVDD28
  N6: Raspberry_Pi1.GPIO27, U1.VALIDV
  N7: Raspberry_Pi1.GPIO22, U1.VALIDH
  N8: Raspberry_Pi1.GPIO10, U1.DOUT_8
  N9: Raspberry_Pi1.GPIO9, U1.DOUT_7
  N10: Raspberry_Pi1.GPIO11, U1.DOUT_6
  N11: Raspberry_Pi1.GPIO8, U1.DOUT_5
  N12: Raspberry_Pi1.GPIO25, U1.DOUT_4
  N13: Raspberry_Pi1.GPIO24, U1.DOUT_2
  N14: Raspberry_Pi1.GPIO23, U1.DOUT_1
  N15: Raspberry_Pi1.GPIO18, U1.DGND
  N16: Raspberry_Pi1.GPIO15, U1.CLK_IN
  N17: Raspberry_Pi1.GPIO14, U1.RESET_N
  N18: Raspberry_Pi1.5V, U1.SCLK, U1.AGND
