# Fritzing sketch id2791_FRITZING_FOR_RIG_0 (saved by Fritzing 0.9.3b)
breadboards: 1

parts:
  SparkFun_Load_Cell_Amplifier_-_HX1 = SparkFun_HX711_Load_Cell [part_number=SEN-13879]
  J1 = Basic Force Sensing Resistor (FSR) [package=THT]
  J2 = Basic Force Sensing Resistor (FSR) [package=THT]
  J3 = Basic Force Sensing Resistor (FSR) [package=THT]
  J4 = Basic Force Sensing Resistor (FSR) [package=THT]
  J5 = Basic Force Sensing Resistor (FSR) [package=THT]
  J6 = Basic Force Sensing Resistor (FSR) [package=THT]
  J7 = Basic Force Sensing Resistor (FSR) [package=THT]
  J8 = Basic Force Sensing Resistor (FSR) [package=THT]
  J9 = Basic Force Sensing Resistor (FSR) [package=THT]
  J10 = Basic Force Sensing Resistor (FSR) [package=THT]
  J11 = Basic Force Sensing Resistor (FSR) [package=THT]
  J12 = Basic Force Sensing Resistor (FSR) [package=THT]
  R1 = Resistor [tolerance=±5% resistance=10k package=THT]
  R2 = Resistor [tolerance=±5% resistance=10k package=THT]
  R3 = Resistor [tolerance=±5% resistance=10k package=THT]
  R4 = Resistor [tolerance=±5% resistance=10k package=THT]
  R5 = Resistor [tolerance=±5% resistance=10k package=THT]
  R6 = Resistor [tolerance=±5% resistance=10k package=THT]
  R7 = Resistor [tolerance=±5% resistance=10k package=THT]
  R8 = Resistor [tolerance=±5% resistance=10k package=THT]
  R9 = Resistor [tolerance=±5% resistance=10k package=THT]
  R10 = Resistor [tolerance=±5% resistance=10k package=THT]
  R11 = Resistor [tolerance=±5% resistance=10k package=THT]
  R12 = Resistor [tolerance=±5% resistance=10k package=THT]
  Part1 = Arduino Mega 2560 (Rev3)
  J13 = LOAD_CELL [package=1x03]
  SparkFun_Load_Cell_Amplifier_-_HX2 = SparkFun_HX711_Load_Cell [part_number=SEN-13879]
  J14 = LOAD_CELL [package=1x03]
  SparkFun_Load_Cell_Amplifier_-_HX3 = SparkFun_HX711_Load_Cell [part_number=SEN-13879]
  J15 = LOAD_CELL [package=1x03]
  SparkFun_Load_Cell_Amplifier_-_HX4 = SparkFun_HX711_Load_Cell [part_number=SEN-13879]
  J16 = LOAD_CELL [package=1x03]

nets:
  N1: SparkFun_Load_Cell_Amplifier_-_HX1.connector17, J1.pin_0, J2.pin_0, J3.pin_0, J4.pin_0, J5.pin_0, J6.pin_0, Part1.5V, SparkFun_Load_Cell_Amplifier_-_HX2.connector17, SparkFun_Load_Cell_Amplifier_-_HX3.connector17, SparkFun_Load_Cell_Amplifier_-_HX4.connector17
  N2: SparkFun_Load_Cell_Amplifier_-_HX1.connector18, Part1.D13_PWM
  N3: SparkFun_Load_Cell_Amplifier_-_HX1.connector19, Part1.D12_PWM
  N4: SparkFun_Load_Cell_Amplifier_-_HX1.connector20, J7.pin_0, J8.pin_0, J9.pin_0, J10.pin_0, J11.pin_0, J12.pin_0, R1.Pin_0, R2.Pin_0, R3.Pin_0, R4.Pin_0, R5.Pin_0, R6.Pin_0, R7.Pin_0, R8.Pin_0, R9.Pin_0, R10.Pin_0, R11.Pin_0, R12.Pin_0, Part1.GND, SparkFun_Load_Cell_Amplifier_-_HX2.connector20, SparkFun_Load_Cell_Amplifier_-_HX3.connector20, SparkFun_Load_Cell_Amplifier_-_HX4.connector20
  N5: SparkFun_Load_Cell_Amplifier_-_HX1.connector25, J13.W
  N6: SparkFun_Load_Cell_Amplifier_-_HX1.connector26, J13.B
  N7: SparkFun_Load_Cell_Amplifier_-_HX1.connector27, J13.R
  N8: J1.pin_1, R1.Pin_1, Part1.A0
  N9: J2.pin_1, R2.Pin_1, Part1.A1
  N10: J3.pin_1, R3.Pin_1, Part1.A2
  N11: J4.pin_1, R4.Pin_1, Part1.A3
  N12: J5.pin_1, R5.Pin_1, Part1.A4
  N13: J6.pin_1, R6.Pin_1, Part1.A5
  N14: J7.pin_1, R12.Pin_1, Part1.A6
  N15: J8.pin_1, R9.Pin_1, Part1.A9
  N16: J9.pin_1, R8.Pin_1, Part1.A10
  N17: J10.pin_1, R7.Pin_1, Part1.A8
  N18: J11.pin_1, R10.Pin_1, Part1.A11
  N19: J12.pin_1, R11.Pin_1, Part1.A7
  N20: Part1.D10_PWM, SparkFun_Load_Cell_Amplifier_-_HX2.connector18
  N21: Part1.D9_PWM, SparkFun_Load_Cell_Amplifier_-_HX2.connector19
  N22: Part1.D3_PWM, SparkFun_Load_Cell_Amplifier_-_HX4.connector19
  N23: Part1.D4_PWM, SparkFun_Load_Cell_Amplifier_-_HX4.connector18
  N24: Part1.D6_PWM, SparkFun_Load_Cell_Amplifier_-_HX3.connector19
  N25: Part1.D7_PWM, SparkFun_Load_Cell_Amplifier_-_HX3.connector18
  N26: SparkFun_Load_Cell_Amplifier_-_HX2.connector25, J14.W
  N27: SparkFun_Load_Cell_Amplifier_-_HX2.connector26, J14.B
  N28: SparkFun_Load_Cell_Amplifier_-_HX2.connector27, J14.R
  N29: SparkFun_Load_Cell_Amplifier_-_HX3.connector25, J15.W
  N30: SparkFun_Load_Cell_Amplifier_-_HX3.connector26, J15.B
  N31: SparkFun_Load_Cell_Amplifier_-_HX3.connector27, J15.R
  N32: SparkFun_Load_Cell_Amplifier_-_HX4.connector25, J16.W
  N33: SparkFun_Load_Cell_Amplifier_-_HX4.connector26, J16.B
  N34: SparkFun_Load_Cell_Amplifier_-_HX4.connector27, J16.R
