# Fritzing sketch id2791_meanwell_V0 (saved by Fritzing 0.9.3b)
breadboards: 1

parts:
  WeMos_D1_Mini1 = WeMos D1 Mini
  U1 = LM358 [package=dip08]
  R1 = Resistor [tolerance=±5% resistance=10k package=THT]
  R2 = Resistor [tolerance=±5% resistance=10k package=THT]
  R3 = Resistor [tolerance=±5% resistance=10k package=THT]
  R4 = Resistor [tolerance=±5% resistance=10k package=THT]
  R6 = Resistor [tolerance=±5% resistance=20k package=THT]
  Power_plug1 = Power plug
  JP2 = Header 2 [package=jst-2-pth-ns]
  R5 = Resistor [tolerance=±5% resistance=20k package=THT]
  JP1 = Header 2 [package=jst-2-pth-ns]

nets:
  N1: WeMos_D1_Mini1.D1, U1.G$1_+IN
  N2: WeMos_D1_Mini1.D2, U1.G$2_+IN
  GND: WeMos_D1_Mini1.G, U1.G$1_V-, R1.Pin_1, R2.Pin_1, R3.Pin_0, R4.Pin_0, Power_plug1.GND, JP2.1, JP1.1
  N3: U1.G$1_OUT, R1.Pin_0, R6.Pin_1, JP1.2
  N4: U1.G$1_-IN, R2.Pin_0, R6.Pin_0
  N5: U1.G$2_-IN, R3.Pin_1, R5.Pin_0
  N6: U1.G$2_OUT, R4.Pin_1, JP2.2, R5.Pin_1
  12V: U1.G$1_V+, Power_plug1.VCC

notes:
  Connect to USB
  DIM-
  DIM+
