# Fritzing sketch id2792_IN_12a_Bus_0 (saved by Fritzing 0.8.7b)
circuit board: 17.6166cm x 4.66125cm

parts:
  U1 = M74HC238 [package=dil16]
  Q1 = NPN-Transistor [part_number=MPSA42 package="TO92 [THT]"]
  R4 = Resistor [tolerance=±5% resistance=1M package=THT]
  R5 = Resistor [tolerance=±5% resistance=10k package=THT]
  Q2 = PNP-Transistor [part_number=MPSA92 package="TO92 [THT]"]
  R7 = Resistor [tolerance=±5% resistance=10k package=THT]
  R8 = Resistor [tolerance=±5% resistance=10k package=THT]
  R9 = Resistor [tolerance=±5% resistance=10k package=THT]
  Q3 = PNP-Transistor [part_number=MPSA92 package="TO92 [THT]"]
  Q4 = NPN-Transistor [part_number=MPSA42 package="TO92 [THT]"]
  R10 = Resistor [tolerance=±5% resistance=10k package=THT]
  R11 = Resistor [tolerance=±5% resistance=10k package=THT]
  R12 = Resistor [tolerance=±5% resistance=10k package=THT]
  R13 = Resistor [tolerance=±5% resistance=10k package=THT]
  R14 = Resistor [tolerance=±5% resistance=1M package=THT]
  Q5 = PNP-Transistor [part_number=MPSA92 package="TO92 [THT]"]
  Q6 = NPN-Transistor [part_number=MPSA42 package="TO92 [THT]"]
  R15 = Resistor [tolerance=±5% resistance=10k package=THT]
  R16 = Resistor [tolerance=±5% resistance=10k package=THT]
  R17 = Resistor [tolerance=±5% resistance=10k package=THT]
  R18 = Resistor [tolerance=±5% resistance=10k package=THT]
  R19 = Resistor [tolerance=±5% resistance=1M package=THT]
  Q7 = PNP-Transistor [part_number=MPSA92 package="TO92 [THT]"]
  Q8 = NPN-Transistor [part_number=MPSA42 package="TO92 [THT]"]
  R20 = Resistor [tolerance=±5% resistance=10k package=THT]
  R21 = Resistor [tolerance=±5% resistance=10k package=THT]
  R22 = Resistor [tolerance=±5% resistance=10k package=THT]
  R23 = Resistor [tolerance=±5% resistance=10k package=THT]
  R24 = Resistor [tolerance=±5% resistance=1M package=THT]
  Q9 = PNP-Transistor [part_number=MPSA92 package="TO92 [THT]"]
  Q10 = NPN-Transistor [part_number=MPSA42 package="TO92 [THT]"]
  R25 = Resistor [tolerance=±5% resistance=10k package=THT]
  R26 = Resistor [tolerance=±5% resistance=10k package=THT]
  R27 = Resistor [tolerance=±5% resistance=10k package=THT]
  R28 = Resistor [tolerance=±5% resistance=10k package=THT]
  R29 = Resistor [tolerance=±5% resistance=1M package=THT]
  Q11 = PNP-Transistor [part_number=MPSA92 package="TO92 [THT]"]
  Q12 = NPN-Transistor [part_number=MPSA42 package="TO92 [THT]"]
  R30 = Resistor [tolerance=±5% resistance=10k package=THT]
  R31 = Resistor [tolerance=±5% resistance=10k package=THT]
  R32 = Resistor [tolerance=±5% resistance=10k package=THT]
  R33 = Resistor [tolerance=±5% resistance=10k package=THT]
  R34 = Resistor [tolerance=±5% resistance=1M package=THT]
  N1 = shrouded pin header, 12 pins [form="♂ (shrouded male)" part_number="IN-12A Connector"]
  N2 = shrouded pin header, 12 pins [form="♂ (shrouded male)" part_number="IN-12A Connector"]
  N3 = shrouded pin header, 12 pins [form="♂ (shrouded male)" part_number="IN-12A Connector"]
  N4 = shrouded pin header, 12 pins [form="♂ (shrouded male)" part_number="IN-12A Connector"]
  N5 = shrouded pin header, 12 pins [form="♂ (shrouded male)" part_number="IN-12A Connector"]
  N6 = shrouded pin header, 12 pins [form="♂ (shrouded male)" part_number="IN-12A Connector"]
  IC2 = IC, DIP package, 16 pins [chip_label=K155ID1 part_number=K155ID1]
  J1 = shrouded pin header, 10 pins [form="♂ (shrouded male)"]

nets:
  N1: U1.A, J1.pin4
  N2: U1.B, J1.pin5
  N3: U1.C, J1.pin6
  GND: U1.~G2A, U1.~G2B, U1.GND, Q1.E, R9.Pin_1, Q4.E, R12.Pin_1, Q6.E, R17.Pin_1, Q8.E, R22.Pin_1, Q10.E, R27.Pin_1, Q12.E, R32.Pin_1, IC2.pin12, J1.pin2
  5V: U1.G1, U1.VCC, IC2.pin5, J1.pin3
  N4: U1.Y7, R7.Pin_0
  N5: U1.Y6, R11.Pin_0
  N6: U1.Y5, R16.Pin_0
  N7: U1.Y4, R21.Pin_0
  N8: U1.Y3, R26.Pin_0
  N9: U1.Y2, R31.Pin_0
  N10: Q1.B, R7.Pin_1, R9.Pin_0
  N11: Q1.C, R4.Pin_0
  N12: R4.Pin_1, Q2.B, R8.Pin_0
  N13: R5.Pin_0, Q2.C
  N14: R5.Pin_1, N1.pin1
  180V: Q2.E, R8.Pin_1, Q3.E, R13.Pin_1, Q5.E, R18.Pin_1, Q7.E, R23.Pin_1, Q9.E, R28.Pin_1, Q11.E, R33.Pin_1, J1.pin1
  N15: Q3.B, R13.Pin_0, R14.Pin_1
  N16: Q3.C, R10.Pin_0
  N17: Q4.B, R11.Pin_1, R12.Pin_0
  N18: Q4.C, R14.Pin_0
  N19: R10.Pin_1, N2.pin1
  N20: Q5.B, R18.Pin_0, R19.Pin_1
  N21: Q5.C, R15.Pin_0
  N22: Q6.B, R16.Pin_1, R17.Pin_0
  N23: Q6.C, R19.Pin_0
  N24: R15.Pin_1, N3.pin1
  N25: Q7.B, R23.Pin_0, R24.Pin_1
  N26: Q7.C, R20.Pin_0
  N27: Q8.B, R21.Pin_1, R22.Pin_0
  N28: Q8.C, R24.Pin_0
  N29: R20.Pin_1, N4.pin1
  N30: Q9.B, R28.Pin_0, R29.Pin_1
  N31: Q9.C, R25.Pin_0
  N32: Q10.B, R26.Pin_1, R27.Pin_0
  N33: Q10.C, R29.Pin_0
  N34: R25.Pin_1, N5.pin1
  N35: Q11.B, R33.Pin_0, R34.Pin_1
  N36: Q11.C, R30.Pin_0
  N37: Q12.B, R31.Pin_1, R32.Pin_0
  N38: Q12.C, R34.Pin_0
  N39: R30.Pin_1, N6.pin1
  N40: N1.pin2, N2.pin2, N3.pin2, N4.pin2, N5.pin2, N6.pin2, IC2.pin16
  N41: N1.pin3, N2.pin3, N3.pin3, N4.pin3, N5.pin3, N6.pin3, IC2.pin2
  N42: N1.pin4, N2.pin4, N3.pin4, N4.pin4, N5.pin4, N6.pin4, IC2.pin1
  N43: N1.pin5, N2.pin5, N3.pin5, N4.pin5, N5.pin5, N6.pin5, IC2.pin10
  N44: N1.pin6, N2.pin6, N3.pin6, N4.pin6, N5.pin6, N6.pin6, IC2.pin11
  N45: N1.pin7, N2.pin7, N3.pin7, N4.pin7, N5.pin7, N6.pin7, IC2.pin14
  N46: N1.pin8, N2.pin8, N3.pin8, N4.pin8, N5.pin8, N6.pin8, IC2.pin13
  N47: N1.pin9, N2.pin9, N3.pin9, N4.pin9, N5.pin9, N6.pin9, IC2.pin9
  N48: N1.pin10, N2.pin10, N3.pin10, N4.pin10, N5.pin10, N6.pin10, IC2.pin8
  N49: N1.pin11, N2.pin11, N3.pin11, N4.pin11, N5.pin11, N6.pin11, IC2.pin15
  N50: IC2.pin3, J1.pin10
  N51: IC2.pin4, J1.pin7
  N52: IC2.pin6, J1.pin9
  N53: IC2.pin7, J1.pin8

notes:
  C
  B
  A
  9
  8
  7
  6
  5
  4
  3
  2
  1
  Nixie Digit 0
  D
