# Fritzing sketch id2797_Power_Supply_2_0 (saved by Fritzing 0.8.7b)
breadboards: 1

parts:
  CONN1 = Power Jack [part_number="12V DC Power supply" package=power_jack_slot]
  D1 = Diode [part_number=1N4007 package=diode-1n4001]
  LED1 = LED - 5mm [color="Green (565nm)" package="5 mm [THT]"]
  R1 = Resistor [tolerance=±5% resistance=330 package=THT]
  U1 = Voltage Regulator - 5V [part_number=LM7805CT package="TO220 [THT]"]
  C1 = Electrolytic Capacitor [capacitance=470µF voltage=16V package="200 mil [THT, electrolytic]"]
  C3 = Ceramic Capacitor [capacitance=1µF package="100 mil [THT, multilayer]"]
  U2 = Voltage Regulator - 3.3V [part_number=LM3940 package="TO220 [THT]"]
  JP1 = Header 2 [part_number="5V for Arduino" package=jst-2-pth-ns]
  C4 = Electrolytic Capacitor [capacitance=33µF package="200 mil [THT, electrolytic]"]
  JP2 = Header 2 [part_number="3.3V for Bluetooth" package=jst-2-pth-ns]
  U3 = MC34063 [part_number=MC34063 package=so08]
  R2 = Resistor [tolerance=±5% resistance=1 package=THT]
  R3 = Resistor [tolerance=±5% resistance=1 package=THT]
  R4 = Resistor [tolerance=±5% resistance=1 package=THT]
  R5 = Resistor [tolerance=±5% resistance=1 package=THT]
  R6 = Resistor [tolerance=±5% resistance=1 package=THT]
  C5 = Electrolytic Capacitor [capacitance=220µF voltage=35V package="300 mil [THT, electrolytic]"]
  L1 = Inductor [inductance=220.0 current=0.90 part_number=18R224C package="400 mil [THT]"]
  D2 = Diode [part_number=1N914 package=diode-1n4001]
  Q1 = PNP-Transistor [part_number=MPSA55 package="TO92 [THT]"]
  R7 = Resistor [tolerance=±5% resistance=1k package=THT]
  Q2 = Basic FET N-Channel [part_number=IRF740 package="TO220 [THT]"]
  D3 = Diode [part_number=BAV21 package=diode-1n4001]
  C6 = Ceramic Capacitor [capacitance=0.1µF package="100 mil [THT, multilayer]"]
  R8 = Resistor [tolerance=±5% resistance=3k package=THT]
  R9 = Resistor [tolerance=±5% resistance=475k package=THT]
  C7 = Ceramic Capacitor [capacitance=2.2nF package="100 mil [THT, multilayer]"]
  C8 = Ceramic Capacitor [capacitance=2.2µF voltage=250V package="100 mil [THT, multilayer]"]
  S1 = Round Pushbutton
  C9 = Electrolytic Capacitor [capacitance=1µF voltage=0.25kV package="200 mil [THT, electrolytic]"]
  D4 = Diode [part_number=MUR140 package=diode-1n4001]
  D5 = Diode [part_number=MUR140 package=diode-1n4001]
  C10 = Electrolytic Capacitor [capacitance=1µF voltage=0.25kV package="200 mil [THT, electrolytic]"]
  C11 = Electrolytic Capacitor [capacitance=1µF voltage=0.25kV package="200 mil [THT, electrolytic]"]
  C12 = Electrolytic Capacitor [capacitance=1µF voltage=0.25kV package="200 mil [THT, electrolytic]"]
  D6 = Diode [part_number=MUR140 package=diode-1n4001]
  D7 = Diode [part_number=MUR140 package=diode-1n4001]
  R10 = Resistor [tolerance=±5% resistance=820k package=THT]
  R11 = Resistor [tolerance=±5% resistance=3.9M package=THT]
  ST1 = Screw terminal - 2 pins [part_number="180V for Nixies" package=THT]
  ST2 = Screw terminal - 2 pins [part_number="450V for Dekatron" package=THT]

nets:
  GND: CONN1.GND, LED1.cathode, U1.GND, C1.-, C3.0, U2.GND, JP1.1, C4.-, JP2.1, U3.GND, C5.-, Q1.C, R7.Pin_0, Q2.source, C6.0, R8.Pin_0, C7.0, C8.0, R11.Pin_0, ST1.pin1, ST2.pin1
  N1: CONN1.PWR, S1.leg0
  N2: D1.A, U3.VCC, R2.Pin_0, R3.Pin_0, R4.Pin_0, R5.Pin_0, R6.Pin_0, S1.leg1
  N3: D1.C, R1.Pin_1, U1.input_voltage, C1.+
  N4: LED1.anode, R1.Pin_0
  N5: U1.output_voltage, C3.1, U2.input_voltage, JP1.2
  N6: U2.output_voltage, C4.+, JP2.2
  N7: U3.SWC, U3.SEN, U3.DVR, R2.Pin_1, R3.Pin_1, R4.Pin_1, R5.Pin_1, R6.Pin_1, C5.+, L1.pin_0
  N8: U3.SWE, D2.A, Q1.B, R7.Pin_1
  N9: U3.TC, C7.1
  N10: U3.COMP, C6.1, R9.Pin_0
  N11: L1.pin_1, Q2.drain, D3.A, C9.-
  N12: D2.C, Q1.E, Q2.gate
  N13: D3.C, R9.Pin_1, C8.1, D5.A, C10.-, ST1.pin2
  N14: C9.+, D4.A, D5.C, C12.-
  N15: D4.C, C10.+, C11.-, D6.A
  N16: C11.+, D7.C, R10.Pin_0
  N17: C12.+, D6.C, D7.A
  N18: R10.Pin_1, R11.Pin_1, ST2.pin2

notes:
  Pulse Out
