# Fritzing sketch id2798_Test_Nixi_Tube_Driver_0 (saved by Fritzing 0.3.13b)
breadboards: 1

parts:
  IC1 = IC, DIP package, 16 pins [chip_label=74141 spacing=300mil]
  IC4 = IC, DIP package, 4 pins [chip_label=IC2 spacing=300mil]
  IC4_2 = IC, DIP package, 4 pins [chip_label=IC3 spacing=300mil]
  IC4_3 = IC, DIP package, 4 pins [chip_label=IC spacing=300mil]
  IC5 = IC, DIP package, 4 pins [chip_label=IC spacing=300mil]
  IC6 = IC, DIP package, 4 pins [chip_label=IC spacing=300mil]
  IC7 = IC, DIP package, 4 pins [chip_label=IC spacing=300mil]
  R1 = Resistor [resistance=1k package=THT]
  R1_2 = Resistor [resistance=1k package=THT]
  R1_3 = Resistor [resistance=1k package=THT]
  R1_4 = Resistor [resistance=1k package=THT]
  R3 = Resistor [resistance=2.2k package=THT]
  only_on_Arduino = Arduino
  R4 = Resistor [resistance=10k package=THT]
  R5 = Resistor [resistance=10k package=THT]
  R6 = Resistor [resistance=10k package=THT]
  R7 = Resistor [resistance=10k package=THT]
  R8 = Resistor [resistance=10k package=THT]
  R9 = Resistor [resistance=10k package=THT]
  R10 = Resistor [resistance=10k package=THT]
  R11 = Resistor [resistance=10k package=THT]
  R12 = Resistor [resistance=10k package=THT]
  R13 = Resistor [resistance=10k package=THT]
  J24 = screw terminal, 9 pins
  J16 = screw terminal, 10 pins
  J26 = female pin header, 6 pins [form="♀ (female rounded)"]

nets:
  N1: IC1.pin1, R4.Pin_1
  N2: IC1.pin2, R5.Pin_1
  N3: IC1.pin3, R1.Pin_1
  N4: IC1.pin4, R1_2.Pin_1
  N5: IC1.pin5, only_on_Arduino.+5V
  N6: IC1.pin6, R1_3.Pin_1
  N7: IC1.pin7, R1_4.Pin_1
  N8: IC1.pin8, R13.Pin_1
  N9: IC1.pin9, R12.Pin_1
  N10: IC1.pin10, R11.Pin_1
  N11: IC1.pin11, R10.Pin_1
  N12: IC1.pin12, R3.Pin_0, only_on_Arduino.GND, J24.pin2
  N13: IC1.pin13, R9.Pin_1
  N14: IC1.pin14, R8.Pin_1
  N15: IC1.pin15, R7.Pin_1
  N16: IC1.pin16, R6.Pin_1
  N17: IC4.pin1, only_on_Arduino.D7
  N18: IC4.pin2, IC4_2.pin2, IC4_3.pin2, IC5.pin2, IC6.pin2, IC7.pin2, R3.Pin_1
  N19: IC4.pin3, J24.pin3
  N20: IC4.pin4, IC4_2.pin4, IC4_3.pin4, IC5.pin4, IC6.pin4, IC7.pin4, J24.pin9
  N21: IC4_2.pin1, only_on_Arduino.D8
  N22: IC4_2.pin3, J24.pin4
  N23: IC4_3.pin1, only_on_Arduino.D9
  N24: IC4_3.pin3, J24.pin5
  N25: IC5.pin1, only_on_Arduino.D10
  N26: IC5.pin3, J24.pin6
  N27: IC6.pin1, only_on_Arduino.D11
  N28: IC6.pin3, J24.pin7
  N29: IC7.pin1, only_on_Arduino.D12
  N30: IC7.pin3, J24.pin8
  N31: R1.Pin_0, only_on_Arduino.D6
  N32: R1_2.Pin_0, only_on_Arduino.D5
  N33: R1_3.Pin_0, only_on_Arduino.D4
  N34: R1_4.Pin_0, only_on_Arduino.D3
  N35: only_on_Arduino.VIN, J24.pin1
  N36: only_on_Arduino.A0, J26.pin1
  N37: only_on_Arduino.A1, J26.pin2
  N38: only_on_Arduino.A2, J26.pin3
  N39: only_on_Arduino.A3, J26.pin4
  N40: only_on_Arduino.A4, J26.pin5
  N41: only_on_Arduino.A5, J26.pin6
  N42: R4.Pin_0, J16.pin1
  N43: R5.Pin_0, J16.pin2
  N44: R6.Pin_0, J16.pin3
  N45: R7.Pin_0, J16.pin4
  N46: R8.Pin_0, J16.pin5
  N47: R9.Pin_0, J16.pin6
  N48: R10.Pin_0, J16.pin7
  N49: R11.Pin_0, J16.pin8
  N50: R12.Pin_0, J16.pin9
  N51: R13.Pin_0, J16.pin10

notes:
  (LEFT)
  VIN
  GND
  Column 1
  Column 2
  Column 3
  Column 4
  Column 5
  Column 6
  170V
  (RIGHT)
  (LEFT)
  Plate 8
  Plate 9
  Plate 0
  Plate 1
  Plate 5
  Plate 4
  Plate 6
  Plate 7
  Plate 3
  Plate 2
  (RIGHT)
