# Fritzing sketch id2799_nixieclock_small_v5.1_0 (saved by Fritzing 0.9.2b)
circuit board: 9.6213cm x 7.55464cm
breadboards: 1

parts:
  J8 = female pin header, 1 pin [form="♀ (female)"]
  Power = male pin header, 2 pins [form="♂ (male)"]
  J6 = female pin header, 8 pins [form="♀ (female)"]
  J9 = female pin header, 2 pins [form="♀ (female)"]
  J7 = female pin header, 3 pins [form="♀ (female)"]
  R1 = Resistor [tolerance=±5% resistance=3.3 package=THT]
  R2 = Resistor [tolerance=±5% resistance=3.3k package=THT]
  R3 = Resistor [tolerance=±5% resistance=3.3k package=THT]
  Q2 = NPN-Transistor [package="TO92 [THT]"]
  Q3 = NPN-Transistor [package="TO92 [THT]"]
  R4 = Resistor [tolerance=±5% resistance=470 package=THT]
  R5 = Resistor [tolerance=±5% resistance=470 package=THT]
  R6 = Resistor [tolerance=±5% resistance=470 package=THT]
  Q4 = NPN-Transistor [package="TO92 [THT]"]
  Q5 = NPN-Transistor [package="TO92 [THT]"]
  R10 = Resistor [tolerance=±5% resistance=100 package=THT]
  R11 = Resistor [tolerance=±5% resistance=100 package=THT]
  R12 = Resistor [tolerance=±5% resistance=100 package=THT]
  R7 = Resistor [tolerance=±5% resistance=15 package=THT]
  R8 = Resistor [tolerance=±5% resistance=15 package=THT]
  R9 = Resistor [tolerance=±5% resistance=15 package=THT]
  J4 = female pin header, 3 pins [form="♀ (female)"]
  J2 = female pin header, 2 pins [form="♀ (female)"]
  J5 = male pin header, 8 pins [form="♂ (male)"]
  LM7805 = Voltage Regulator - 5V [package="TO220 [THT]"]
  Q6 = NPN-Transistor [package="TO92 [THT]"]
  K155ID1 = K155ID1-es
  K155ID1_2 = K155ID1-es
  8563p = IC, DIP package, 8 pins [chip_label="8563 RTC"]
  R13 = Resistor [tolerance=±5% resistance=2.2 package=THT]
  R14 = Resistor [tolerance=±5% resistance=2.2 package=THT]
  C1 = Ceramic Capacitor [capacitance=0.1µF package="100 mil [THT, multilayer]"]
  XTAL1 = Crystal [frequency="32 MHz" package=THT]
  Q1 = NPN-Transistor [package="TO92 [THT]"]
  Trinket_Pro = trinketpro 5.0
  BLUEFRUIT1 = Adafruit_Bluefruit_EZ_LINK_v1.0

nets:
  N1: J8.pin1, K155ID1.connector7
  N2: Power.pin1, LM7805.input_voltage
  N3: Power.pin2, Q2.E, Q3.E, J2.pin1, LM7805.GND, K155ID1.connector11, K155ID1_2.connector11, Q1.E, Trinket_Pro.connector76, BLUEFRUIT1.connector2
  N4: J6.pin1, K155ID1_2.connector8
  N5: J6.pin2, K155ID1_2.connector9
  N6: J6.pin3, K155ID1_2.connector10
  N7: J6.pin5, K155ID1_2.connector12
  N8: J6.pin6, K155ID1_2.connector13
  N9: J6.pin7, K155ID1_2.connector14
  N10: J6.pin8, K155ID1_2.connector15
  N11: J9.pin1, K155ID1_2.connector0
  N12: J9.pin2, K155ID1_2.connector1
  N13: J7.pin1, K155ID1.connector1
  N14: J7.pin2, K155ID1.connector0
  N15: J7.pin3, K155ID1_2.connector7
  N16: R1.Pin_0, Trinket_Pro.connector98
  N17: R1.Pin_1, Q1.B
  N18: R2.Pin_0, Trinket_Pro.connector97
  N19: R2.Pin_1, Q2.B
  N20: R3.Pin_0, Trinket_Pro.connector96
  N21: R3.Pin_1, Q3.B
  N22: Q2.C, R5.Pin_0
  N23: Q3.C, R6.Pin_0
  N24: R4.Pin_0, Q1.C
  N25: R4.Pin_1, Q4.C, J4.pin1
  N26: R5.Pin_1, Q5.B, R11.Pin_1
  N27: R6.Pin_1, R12.Pin_0, R9.Pin_0, Q6.B
  N28: Q4.E, Q4.B, R10.Pin_1
  N29: Q5.E, R11.Pin_0
  N30: Q5.C, J4.pin2
  N31: R10.Pin_0, R7.Pin_0
  N32: R12.Pin_1, Q6.E
  N33: R7.Pin_1, R8.Pin_0, J2.pin2
  N34: R8.Pin_1, R9.Pin_1
  N35: J4.pin3, Q6.C
  N36: J5.pin1, K155ID1.connector8
  N37: J5.pin2, K155ID1.connector9
  N38: J5.pin3, K155ID1.connector10
  N39: J5.pin5, K155ID1.connector12
  N40: J5.pin6, K155ID1.connector13
  N41: J5.pin7, K155ID1.connector14
  N42: J5.pin8, K155ID1.connector15
  N43: LM7805.output_voltage, K155ID1.connector4, K155ID1_2.connector4, 8563p.pin8, R13.Pin_1, R14.Pin_1, Trinket_Pro.connector75, BLUEFRUIT1.connector4
  N44: K155ID1.connector2, Trinket_Pro.connector80
  N45: K155ID1.connector3, Trinket_Pro.connector81
  N46: K155ID1.connector5, Trinket_Pro.connector82
  N47: K155ID1.connector6, Trinket_Pro.connector83
  N48: K155ID1_2.connector2, Trinket_Pro.connector91
  N49: K155ID1_2.connector3, Trinket_Pro.connector92
  N50: K155ID1_2.connector5, Trinket_Pro.connector93
  N51: K155ID1_2.connector6, Trinket_Pro.connector79
  N52: 8563p.pin1, XTAL1.pin_1
  N53: 8563p.pin2, C1.0, XTAL1.pin_0
  N54: 8563p.pin4, C1.1
  N55: 8563p.pin5, R14.Pin_0, Trinket_Pro.connector99
  N56: 8563p.pin6, R13.Pin_0, Trinket_Pro.connector100
  N57: Trinket_Pro.connector84, BLUEFRUIT1.connector6
  N58: Trinket_Pro.connector85, BLUEFRUIT1.connector5

notes:
  esHeavyIndustries
