# Fritzing sketch id27_10_led_and_2_shift_register_0 (saved by Fritzing 0.8.0b)
breadboards: 1

parts:
  U1 = 74HC595 [package="DIP16 [THT]"]
  U2 = 74HC595 [package="DIP16 [THT]"]
  Part1 = Arduino Uno (Rev3)
  LED1 = LED - 5mm [color="Red (633nm)" package="5 mm [THT]"]
  LED2 = LED - 5mm [color="Red (633nm)" package="5 mm [THT]"]
  LED3 = LED - 5mm [color="Red (633nm)" package="5 mm [THT]"]
  LED4 = LED - 5mm [color="Red (633nm)" package="5 mm [THT]"]
  LED5 = LED - 5mm [color="Red (633nm)" package="5 mm [THT]"]
  LED6 = LED - 5mm [color="Red (633nm)" package="5 mm [THT]"]
  LED7 = LED - 5mm [color="Red (633nm)" package="5 mm [THT]"]
  LED8 = LED - 5mm [color="Red (633nm)" package="5 mm [THT]"]
  LED9 = LED - 5mm [color="Red (633nm)" package="5 mm [THT]"]
  LED10 = LED - 5mm [color="Red (633nm)" package="5 mm [THT]"]
  R1 = Resistor [tolerance=±5% resistance=220 package=THT]
  R2 = Resistor [tolerance=±5% resistance=220 package=THT]
  R3 = Resistor [tolerance=±5% resistance=220 package=THT]
  R4 = Resistor [tolerance=±5% resistance=220 package=THT]
  R5 = Resistor [tolerance=±5% resistance=220 package=THT]
  R6 = Resistor [tolerance=±5% resistance=220 package=THT]
  R7 = Resistor [tolerance=±5% resistance=220 package=THT]
  R8 = Resistor [tolerance=±5% resistance=220 package=THT]
  R9 = Resistor [tolerance=±5% resistance=220 package=THT]
  R10 = Resistor [tolerance=±5% resistance=220 package=THT]
  C1 = Tantalum Capacitor [capacitance="1 μF" package="100 mil [THT, tantalum]"]

nets:
  N1: U1.Q1, LED2.cathode
  N2: U1.Q2, LED3.cathode
  N3: U1.Q3, LED4.cathode
  N4: U1.Q4, LED5.cathode
  N5: U1.Q5, LED6.cathode
  N6: U1.Q6, LED7.cathode
  N7: U1.Q7, LED8.cathode
  GND: U1.GND, U1.OE, U2.GND, U2.OE, Part1.GND, R1.Pin_0, R2.Pin_0, R3.Pin_0, R4.Pin_0, R5.Pin_0, R6.Pin_0, R7.Pin_0, R8.Pin_0, R9.Pin_0, R10.Pin_0, C1.-
  N8: U1.Q7', U2.DS
  VCC: U1.MR, U1.VCC, U2.MR, U2.VCC, Part1.5V
  N9: U1.SH_CP, U2.SH_CP, Part1.D12/MISO
  N10: U1.ST_CP, U2.ST_CP, Part1.D8, C1.+
  N11: U1.DS, Part1.D11_PWM/MOSI
  N12: U1.Q0, LED1.cathode
  N13: U2.Q1, LED10.cathode
  N14: U2.Q0, LED9.cathode
  N15: LED1.anode, R1.Pin_1
  N16: LED2.anode, R3.Pin_1
  N17: LED3.anode, R4.Pin_1
  N18: LED4.anode, R5.Pin_1
  N19: LED5.anode, R6.Pin_1
  N20: LED6.anode, R7.Pin_1
  N21: LED7.anode, R8.Pin_1
  N22: LED8.anode, R9.Pin_1
  N23: LED9.anode, R10.Pin_1
  N24: LED10.anode, R2.Pin_1
