# Fritzing sketch id2800_Placa_shield_para_proyecto_selladoras_0 (saved by Fritzing 0.9.3b)
circuit board: 10.16cm x 5.36194cm

parts:
  U1 = PIN DIGITAL 1X18
  U3 = PWM 2
  COMUNICACIÓN_1 = COMUNICACIÓN 2
  pwm_1 = PWM 2
  S1 = Pushbutton [package="[THT]"]
  SALIDA_DE_VOLTAJE_5V_3_3V_GND1 = VCC PIN
  U4 = EB-85A Connector [package=eb-85a]
  JP5 = Header 6 [package=em406]
  JP4 = Header 6 [package=em406]
  FUENTE_GND_5V_3_3V1 = VCC
  FUENTE_GND_5V_3_3V2 = VCC
  FUENTE_GND_5V_3_3V3 = VCC

nets:
  N1: U1.connector1, FUENTE_GND_5V_3_3V2.connector5
  N2: U1.connector2, FUENTE_GND_5V_3_3V2.connector4
  N3: U1.connector3, FUENTE_GND_5V_3_3V2.connector3
  N4: U1.connector5, FUENTE_GND_5V_3_3V2.connector2
  N5: U1.connector6, FUENTE_GND_5V_3_3V3.connector5
  N6: U1.connector7, FUENTE_GND_5V_3_3V3.connector4
  N7: U1.connector8, FUENTE_GND_5V_3_3V3.connector3
  N8: U1.connector10, FUENTE_GND_5V_3_3V3.connector2
  N9: U3.connector1, JP5.3
  N10: U3.connector2, JP5.2
  N11: U3.connector3, JP5.1
  N12: COMUNICACIÓN_1.connector6, JP4.5
  N13: COMUNICACIÓN_1.connector7, JP4.6
  N14: pwm_1.connector0, FUENTE_GND_5V_3_3V1.connector5
  N15: pwm_1.connector1, FUENTE_GND_5V_3_3V1.connector4
  N16: pwm_1.connector2, FUENTE_GND_5V_3_3V1.connector3
  N17: pwm_1.connector3, FUENTE_GND_5V_3_3V1.connector2
  N18: pwm_1.connector4, FUENTE_GND_5V_3_3V1.connector1
  N19: pwm_1.connector5, FUENTE_GND_5V_3_3V1.connector0
  N20: S1.Pin_1, S1.Pin_2, SALIDA_DE_VOLTAJE_5V_3_3V_GND1.connector2, U4.RX1
  N21: S1.Pin_3, S1.Pin_4, SALIDA_DE_VOLTAJE_5V_3_3V_GND1.connector3, SALIDA_DE_VOLTAJE_5V_3_3V_GND1.connector5, U4.VCC, U4.TX1, JP5.5, JP4.2, FUENTE_GND_5V_3_3V1.connector6, FUENTE_GND_5V_3_3V2.connector1, FUENTE_GND_5V_3_3V3.connector6
  N22: SALIDA_DE_VOLTAJE_5V_3_3V_GND1.connector0, U4.RX2
  N23: SALIDA_DE_VOLTAJE_5V_3_3V_GND1.connector1, U4.TX2, U4.PPS, U4.BATT, JP5.6, JP4.4, FUENTE_GND_5V_3_3V1.connector7, FUENTE_GND_5V_3_3V2.connector6, FUENTE_GND_5V_3_3V3.connector1
  N24: SALIDA_DE_VOLTAJE_5V_3_3V_GND1.connector4, U4.GND
