# Fritzing sketch id2802_no_usb_arduino_stripboard_0 (saved by Fritzing 0.9.2b)
stripboards: 1

parts:
  U1 = atmega328 [package=dip]
  J1 = female pin header, 14 pins [form="♀ (female)"]
  IC1 = Voltage Regulator [package=78xxl]
  C1 = Electrolytic Capacitor [capacitance=220µF voltage=20V package="100 mil [THT, electrolytic]"]
  R1 = Resistor [tolerance=±5% resistance=220 package=THT]
  S1 = Pushbutton [package="[THT]"]
  R3 = Resistor [tolerance=±5% resistance=10k package=THT]
  C5 = Ceramic Capacitor [capacitance=100nF package="100 mil [THT, multilayer]"]
  D1 = Rectifier Diode [part_number=1N4007 package="300 mil [THT]"]
  XTAL1 = Crystal [frequency="16 Mhz" package=THT]
  C6 = Ceramic Capacitor [capacitance=22pF package="100 mil [THT, multilayer]"]
  C7 = Ceramic Capacitor [capacitance=22pF package="100 mil [THT, multilayer]"]
  R4 = Resistor [tolerance=±5% resistance=180 package=THT]
  LED3 = LED - 5mm [color="Yellow (585nm)" package="5 mm [THT]"]
  J2 = female pin header, 8 pins [form="♀ (female)"]
  J8 = female pin header, 4 pins [form="♀ (female)"]
  J10 = female pin header, 3 pins [form="♀ (female)"]
  V1 = DC Power [voltage=5]
  C8 = Ceramic Capacitor [capacitance=100nF package="100 mil [THT, multilayer]"]
  LED4 = LED - 5mm [color="Green (555nm)" package="5 mm [THT]"]
  J11 = female pin header, 6 pins [form="♀ (female)"]

nets:
  N1: U1.RESET, S1.Pin_1, S1.Pin_2, R3.Pin_1, J2.pin1, J10.pin1
  N2: U1.D0_(RX), J2.pin2, J10.pin2
  N3: U1.D1_(TX), J2.pin3, J10.pin3
  N4: U1.D2, J2.pin4
  N5: U1.D3_(PWM), J2.pin5
  N6: U1.D4, J2.pin6
  N7: U1.VCC, U1.AVCC, U1.AREF, J1.pin8, J1.pin9, IC1.OUT, R1.Pin_1, R3.Pin_0, C5.1, J2.pin7, C8.1, J11.pin1, J11.pin2
  GND: U1.GND, J1.pin7, IC1.GND, C1.-, S1.Pin_3, S1.Pin_4, C5.0, C6.1, C7.1, R4.Pin_0, J2.pin8, V1.V+, C8.0, LED4.cathode
  N8: U1.XLAT1, XTAL1.pin_1, C7.0
  N9: U1.XLAT2, XTAL1.pin_0, C6.0
  N10: U1.D5_(PWM), J8.pin1
  N11: U1.D6_(PWM), J8.pin2
  N12: U1.D7, J8.pin3
  N13: U1.D8, J8.pin4
  N14: U1.D9_(PWM), J1.pin14
  N15: U1.D10_(PWM), J1.pin13, J11.pin6
  N16: U1.D11_(PWM), J1.pin12, J11.pin5
  N17: U1.D12, J1.pin11, J11.pin4
  N18: U1.D13, J1.pin10, LED3.anode, J11.pin3
  N19: U1.A0, J1.pin6
  N20: U1.A1, J1.pin5
  N21: U1.A2, J1.pin4
  N22: U1.A3, J1.pin3
  N23: U1.A4, J1.pin2
  N24: U1.A5, J1.pin1
  N25: IC1.IN, C1.+, D1.cathode
  N26: R1.Pin_0, LED4.anode
  N27: D1.anode, V1.V-
  N28: R4.Pin_1, LED3.cathode

notes:
  ABCDEFGHIJK
  Ignore this first line if you have a 19x29 board.
  Most Vero Boards are 18x33,
  Some are 19x29
  This circuit is based on 18x33 boards.
  You Need 18x18.
