# Fritzing sketch id2803_projekt1_0 (saved by Fritzing 0.9.3b)
perfboards: 1

parts:
  IC1 = Voltage Regulator [part_number=LM7805 package=78xxl]
  Power_plug1 = Power plug
  C1 = Electrolytic Capacitor [capacitance=10µF package="0405 [SMD, electrolytic]"]
  C2 = Electrolytic Capacitor [capacitance=10µF package="0405 [SMD, electrolytic]"]
  R1 = Resistor [tolerance=±5% resistance=10k package=THT]
  XTAL1 = Crystal [frequency="16 Mhz" package=THT]
  C3 = Ceramic Capacitor [capacitance=22pF package="0805 [SMD, multilayer]"]
  C4 = Ceramic Capacitor [capacitance=22pF package="0805 [SMD, multilayer]"]
  C5 = Ceramic Capacitor [capacitance="100 nF" package="0805 [SMD, multilayer]"]
  C6 = Ceramic Capacitor [capacitance="100 nF" package="0805 [SMD, multilayer]"]
  JP1 = Header 5x2 [part_number="AVR ISP" package=avr_icsp]
  U1 = atmega168 [package=dip]
  U1_2 = atmega328 [package=dip]
  LED1 = LED - 5mm [color="Green (560nm)" package="5 mm [THT]"]
  R2 = Resistor [tolerance=±5% resistance=220 package=THT]
  IC2 = L293D [package=THT]
  Q1 = PNP-Transistor [package="TO92 [THT]"]
  R3 = Resistor [tolerance=±5% resistance=1k package=THT]
  S1 = Pushbutton [package=THT]
  J1 = Screw terminal - 2 pins [part_number=MOTOR1 package=THT]
  J2 = screw terminal, 2 pins
  J2_2 = Screw terminal - 2 pins [part_number=MOTOR2 package=THT]
  Q2 = PNP-Transistor [package="TO92 [THT]"]
  R4 = Resistor [tolerance=±5% resistance=1k package=THT]
  S2 = Pushbutton [package=THT]
  Q3 = PNP-Transistor [package="TO92 [THT]"]
  R5 = Resistor [tolerance=±5% resistance=1k package=THT]
  S3 = Pushbutton [package=THT]

nets:
  GND: IC1.GND, Power_plug1.GND, C1.-, C2.-, C3.1, C4.1, C5.0, C6.0, JP1.4, JP1.6, JP1.8, JP1.10, U1.GND, U1_2.GND, R2.Pin_1, IC2.0V, R3.Pin_1, S1.leg1, R4.Pin_1, S2.leg1, R5.Pin_1, S3.leg1
  N1: IC1.IN, Power_plug1.VCC, C1.+, IC2.+Vmotor
  VCC: IC1.OUT, C2.+, R1.Pin_1, C5.1, C6.1, JP1.2, U1.VCC, U1.AVCC, U1_2.VCC, U1_2.AVCC, IC2.+V, Q1.E, Q2.E, Q3.E
  N2: R1.Pin_0, U1.RESET
  N3: XTAL1.pin_0, C3.0, U1.XLAT1, U1_2.XLAT1
  N4: XTAL1.pin_1, C4.0, U1.XLAT2, U1_2.XLAT2
  N5: JP1.1, U1_2.D11_(PWM)
  N6: JP1.5, U1_2.RESET
  N7: JP1.7, U1_2.D13, LED1.cathode
  N8: JP1.9, U1_2.D12
  N9: U1_2.D2, IC2.In_1
  N10: U1_2.D4, IC2.In_2
  N11: U1_2.D5_(PWM), IC2.Enable_2
  N12: U1_2.D6_(PWM), IC2.Enable_1
  N13: U1_2.D7, IC2.In_4
  N14: U1_2.D8, IC2.In_3
  N15: U1_2.A3, Q3.C, R5.Pin_0
  N16: U1_2.A4, Q2.C, R4.Pin_0
  N17: U1_2.A5, Q1.C, R3.Pin_0
  N18: LED1.anode, R2.Pin_0
  N19: IC2.Out_1_(_Controlled_by_Enable_1_), J1.pin2
  N20: IC2.Out_2_(_Controlled_by_Enable_1_), J1.pin1
  N21: IC2.Out_3_(_Controlled_by_Enable_2_), J2.pin2, J2_2.pin2
  N22: IC2.Out_4_(_Controlled_by_Enable_2_), J2.pin1, J2_2.pin1
  N23: Q1.B, S1.leg0
  N24: Q2.B, S2.leg0
  N25: Q3.B, S3.leg0
