# Fritzing sketch id2804_infra_0 (saved by Fritzing 0.9.3b)
breadboards: 1

parts:
  Raspberry_Pi_1 = Raspberry Pi 3 [part_number=RPI-3-V1.2]
  R1 = Resistor [tolerance=±5% resistance=220 package=THT]
  LED1 = LED - 5mm [color="Red (633nm)" package="5 mm [THT]"]
  Q1 = NPN-Transistor [package="TO92 [THT]"]
  LED2 = LED - 5mm [color="Red (633nm)" package="5 mm [THT]"]
  LED3 = LED - 5mm [color="Red (633nm)" package="5 mm [THT]"]
  LED4 = LED - 5mm [color="Red (633nm)" package="5 mm [THT]"]
  LED5 = LED - 5mm [color="Red (633nm)" package="5 mm [THT]"]
  LED6 = LED - 5mm [color="Red (633nm)" package="5 mm [THT]"]
  R2 = Resistor [tolerance=±5% resistance=220 package=THT]
  PIR1 = PIR_sensor

nets:
  N1: Raspberry_Pi_1.GPIO4, PIR1.connector2
  N2: Raspberry_Pi_1.GND, Q1.E, PIR1.connector3
  N3: Raspberry_Pi_1.GPIO23, Q1.B
  N4: Raspberry_Pi_1.5V, R1.Pin_0, R2.Pin_0, PIR1.connector1
  N5: R1.Pin_1, LED3.anode
  N6: LED1.cathode, LED2.anode
  N7: LED1.anode, LED3.cathode
  N8: Q1.C, LED2.cathode, LED4.cathode
  N9: LED4.anode, LED6.cathode
  N10: LED5.cathode, LED6.anode
  N11: LED5.anode, R2.Pin_1
