# Fritzing sketch id2805_node_pi_softshutdown_0 (saved by Fritzing 0.9.2b)
breadboards: 1

parts:
  Raspberry_Pi1 = Raspberry Pi 2
  S1 = Pushbutton [package=THT]
  R1 = Resistor [tolerance=±5% resistance=1k package="2010 [SMD]"]
  R2 = Resistor [tolerance=±5% resistance=10k package="2010 [SMD]"]

nets:
  N1: Raspberry_Pi1.3v3, S1.leg0
  N2: Raspberry_Pi1.GPIO4, R1.Pin_0
  N3: Raspberry_Pi1.GND, R2.Pin_0
  N4: S1.leg1, R1.Pin_1, R2.Pin_1

notes:
  10 KOhm resostor goes to ground and 1KOhm goes to GPIO4
