# Fritzing sketch id2807_Thingspeak_DS18B20_0 (saved by Fritzing 0.9.3b)
breadboards: 1

parts:
  DS1 = DS18B20 1-Wire Temperature Sensor [part_number=DS18B20]
  WeMos_D1_Mini1 = WeMos D1 Mini

nets:
  N1: DS1.GND, WeMos_D1_Mini1.G
  N2: DS1.DQ, WeMos_D1_Mini1.D4
  VDD: DS1.VDD, WeMos_D1_Mini1.3V3
