# Fritzing sketch id280_Alarme_0 (saved by Fritzing 0.9.3b)
perfboards: 1

parts:
  J1 = Camdenboss CTB0158-3 [part_number=CTB0158-3 package=THT]
  LED1 = LED - 5mm [color="Red (633nm)" package="5 mm [THT]"]
  LED2 = LED - 5mm [color="Green (555nm)" package="5 mm [THT]"]
  R3 = Resistor [tolerance=±5% resistance=220 package=THT]
  S3 = Round Pushbutton
  U2 = RELAY [package=relay-jzc]
  R4 = Resistor [tolerance=±5% resistance=220 package=THT]
  S5 = Pushbutton [package=THT]
  J2 = Piezo Speaker

nets:
  N1: J1.pin1, S3.leg0
  N2: J1.pin3, U2.COIL2
  N3: LED1.anode, R4.Pin_1
  N4: LED2.anode, R3.Pin_1
  N5: S3.leg1, U2.COIL1, S5.leg0
  N6: U2.NC, J2.pin2
  N7: U2.NO, R4.Pin_0

notes:
  Porte
  Serrure
