# Fritzing sketch id2811_esp_with_arduino_and_voltage_divider_0 (saved by Fritzing 0.9.1b)
breadboards: 1

parts:
  Part1 = Spark Core (v1.0)
  Part2 = Arduino Mega 2560 (Rev3)
  R1 = Resistor [tolerance=±5% resistance=100 package=THT]
  R2 = Resistor [tolerance=±5% resistance=100 package=THT]  # not connected
  R3 = Resistor [tolerance=±5% resistance=100 package=THT]

nets:
  N1: Part1.TX, Part2.D19/RX1
  N2: Part1.RX, R1.Pin_1
  N3: Part2.D18/TX1, R1.Pin_0
  N4: Part2.GND, R3.Pin_1
