# Fritzing sketch id2813_nodemcu_Sdcard_0 (saved by Fritzing 0.9.3b)

parts:
  U1 = NodeMCU
  SD1 = SD Card [part_number=sdcard]

nets:
  N1: U1.connector2, SD1.connector4
  N2: U1.connector5, SD1.connector7
  N3: U1.connector6, SD1.connector6, SD1.connector9
  N4: U1.connector7, SD1.connector8
  N5: U1.connector8, SD1.connector10
  N6: U1.connector9, SD1.connector5
