# Fritzing sketch id2814_Digram_0 (saved by Fritzing 0.9.3b)

parts:
  Gizwits_WiFi_Witty_ESP-12F1 = Gizwits WiFi Witty ESP-12F
  KY-1 = keyes
  LED1 = smd LED [color="Red (633nm)" package="0805 [SMD]"]  # not connected

nets:
  N1: Gizwits_WiFi_Witty_ESP-12F1.GND, KY-1.connector1
  N2: Gizwits_WiFi_Witty_ESP-12F1.GPIO0, KY-1.connector0
