# Fritzing sketch id2817_Noisy_Cricket_MkII_v2_1_0 (saved by Fritzing 0.8.0b)
breadboards: 1

parts:
  4_7k = Resistor [tolerance=±5% resistance=220 package=THT]
  1M = Resistor [tolerance=±5% resistance=220 package=THT]
  3_3k = Resistor [tolerance=±5% resistance=220 package=THT]
  25k = Trimmer Potentiometer [maximum_resistance=100kΩ package=THT]
  100n = Resistor [tolerance=±5% resistance=220 package=THT]
  100n_2 = Resistor [tolerance=±5% resistance=220 package=THT]
  100n_3 = Resistor [tolerance=±5% resistance=220 package=THT]
  100n_4 = Resistor [tolerance=±5% resistance=220 package=THT]
  LM386 = LM 358 Dual Op-Amp [package="DIP8 [THT]"]
  47n = Resistor [tolerance=±5% resistance=220 package=THT]
  47n_2 = Resistor [tolerance=±5% resistance=220 package=THT]
  MPF102 = transistor_signal_NPN_TO92.fzp
  GUITAR = mystery part, 2 pins [chip_label=?]
  10k_VOL = Rotary Potentiometer (Large) [maximum_resistance=10kΩ package=THT]
  100k_TONE = Rotary Potentiometer (Large) [maximum_resistance=10kΩ package=THT]
  1k_GAIN = Rotary Potentiometer (Large) [maximum_resistance=10kΩ package=THT]
  220μF = Electrolytic Capacitor [capacitance=1µF package="100 mil [THT, electrolytic]"]
  220μF_2 = Electrolytic Capacitor [capacitance=1µF package="100 mil [THT, electrolytic]"]
  SPK = mystery part, 2 pins [chip_label=?]
  10R = Resistor [tolerance=±5% resistance=220 package=THT]
  BOOST = mystery part, 2 pins [chip_label=?]
  9-12V = mystery part, 2 pins [chip_label=?]
  SW = mystery part, 2 pins [chip_label=?]
  LED = LED - 3mm [color="Red (633nm)" package="3 mm [THT]"]
  AUX = mystery part, 2 pins [chip_label=?]
  JP1 = mystery part, 2 pins [chip_label=?]
  JP2 = mystery part, 2 pins [chip_label=?]
  R2 = Resistor [tolerance=±5% resistance=220 package=THT]
  PHONES = mystery part, 4 pins [chip_label=?]
  22k = Resistor [tolerance=±5% resistance=220 package=THT]
  3_9k = Resistor [tolerance=±5% resistance=220 package=THT]
  JP3 = mystery part, 2 pins [chip_label=?]

nets:
  N1: 4_7k.Pin_0, LED.anode
  N2: 4_7k.Pin_1, LM386.connector5, MPF102.connector0, 220μF.+, SW.pin2
  N3: 1M.Pin_0, MPF102.connector2, GUITAR.pin1
  N4: 1M.Pin_1, 3_3k.Pin_1, 100n_2.Pin_0, 100n_4.Pin_0, LM386.connector2, LM386.connector3, 47n_2.Pin_1, GUITAR.pin2, 10k_VOL.leg2, 220μF.-, SPK.pin2, 9-12V.pin2, LED.cathode, JP2.pin1, R2.Pin_0, PHONES.pin4, 22k.Pin_0
  N5: 3_3k.Pin_0, 47n.Pin_0, MPF102.connector1
  N6: 25k.leg1, JP1.pin2
  N7: 25k.wiper, AUX.pin1
  N8: 25k.leg2, JP2.pin2
  N9: 100n.Pin_0, JP1.pin1, 3_9k.Pin_1, JP3.pin2
  N10: 100n.Pin_1, 10k_VOL.wiper, 100k_TONE.leg2
  N11: 100n_2.Pin_1, 100k_TONE.leg1, 100k_TONE.wiper
  N12: 100n_3.Pin_0, LM386.connector4, 220μF_2.+, 10R.Pin_0
  N13: 100n_3.Pin_1, BOOST.pin1
  N14: 100n_4.Pin_1, LM386.connector6, BOOST.pin2
  N15: LM386.connector0, 1k_GAIN.leg1
  N16: LM386.connector1, 3_9k.Pin_0, JP3.pin1
  N17: LM386.connector7, 1k_GAIN.wiper, 1k_GAIN.leg2
  N18: 47n.Pin_1, 10k_VOL.leg1
  N19: 47n_2.Pin_0, 10R.Pin_1
  N20: 220μF_2.-, PHONES.pin1
  N21: SPK.pin1, PHONES.pin2
  N22: 9-12V.pin1, SW.pin1
  N23: AUX.pin2, 22k.Pin_1
  N24: R2.Pin_1, PHONES.pin3

notes:
  ©2013
  Antonis Maglaras
  Noisy Cricket Mk.II
  Version 2
  +
  Trimmer
