# Fritzing sketch id2819_lcd_dht11_0 (saved by Fritzing 0.9.0b)
breadboards: 1

parts:
  Part1 = Arduino Uno (Rev3)
  DHT1 = DHT11_Temperature_and_Humitidy_Sensor
  Nokia_5110_LCD_Module4 = Nokia5110 84x48
  Nokia_5110_LCD_Module5 = Nokia5110LCDModule

nets:
  N1: Part1.D2, DHT1.connector2
  N2: Part1.D3_PWM, Nokia_5110_LCD_Module4.connector3, Nokia_5110_LCD_Module5.connector0
  N3: Part1.D5_PWM, Nokia_5110_LCD_Module4.connector4, Nokia_5110_LCD_Module5.connector2
  N4: Part1.D6_PWM, Nokia_5110_LCD_Module4.connector5, Nokia_5110_LCD_Module5.connector3
  N5: Part1.D7, Nokia_5110_LCD_Module4.connector6, Nokia_5110_LCD_Module5.connector4
  N6: Part1.3V3, Nokia_5110_LCD_Module4.connector0, Nokia_5110_LCD_Module5.connector5
  N7: Part1.5V, DHT1.connector1, Nokia_5110_LCD_Module4.connector7, Nokia_5110_LCD_Module5.connector6
  N8: Part1.GND, DHT1.connector4, Nokia_5110_LCD_Module4.connector1, Nokia_5110_LCD_Module5.connector7
  N9: Nokia_5110_LCD_Module4.connector2, Nokia_5110_LCD_Module5.connector1
