# Fritzing sketch id281_alarm_circuit_with_buzzer_5v_0 (saved by Fritzing 0.9.2b)
circuit board: 4.67182cm x 2.26721cm
breadboards: 1

parts:
  Raspberry_Pi1 = Raspberry Pi B+
  Q1 = TRANSISTOR_NPN [part_number=2N2222 package=to-92-ammo]
  J1 = Piezo Speaker
  VCC1 = 4 x AAA Battery Mount
  R1 = Resistor [tolerance=±5% resistance=10k package="0603 [SMD]"]
  R2 = Resistor [tolerance=±5% resistance=10k package="0603 [SMD]"]
  LED1 = smd LED [color="Green (570nm)" package="0603 [SMD]"]
  JP1 = Header 3 [package=molex-1x3_lock]

nets (from the pcb view):
  N1: Raspberry_Pi1.GPIO24, Q1.E, VCC1.+, R1.Pin_1, R2.Pin_0, LED1.anode, JP1.3
  N2: Q1.B, R2.Pin_1
  N3: Q1.C, J1.pin1
  N4: J1.pin2, JP1.2
  N5: VCC1.-, R1.Pin_0, LED1.cathode, JP1.1
