# Fritzing sketch id2820_pierdolnik_0 (saved by Fritzing 0.9.3b)

parts:
  Part1 = Real Time Clock Module - DS1307 RTC Breakout Board
  LCD1 = LCD screen
  Part3 = Arduino Uno (Rev3)
  Part2 = MicroSD Card Module
  R1 = Resistor [tolerance=±5% resistance=4.7k package="1206 [SMD]"]
  R3 = Trimmer Potentiometer [maximum_resistance=10kΩ package=THT]
  DS1 = DS18B20 1-Wire Temperature Sensor [part_number=DS18B20]

nets:
  5V: Part1.5V, LCD1.VDD, Part3.5V, R1.Pin_1, R3.leg1, DS1.VDD
  GND: Part1.GND, LCD1.VSS, Part3.GND, R3.leg2, DS1.GND
  N1: Part1.SCL, Part3.A5/SCL
  N2: Part1.SDA, Part3.A4/SDA
  N3: LCD1.V0, R3.wiper
  N4: LCD1.RS, Part3.D12/MISO
  N5: LCD1.E, Part3.D11_PWM/MOSI
  N6: LCD1.DB4, Part3.D6_PWM
  N7: LCD1.DB5, Part3.D5_PWM
  N8: LCD1.DB6, Part3.D4
  N9: LCD1.DB7, Part3.D3_PWM
  N10: Part3.D9_PWM, Part2.CS
