# Fritzing sketch id2821_nostromotron_modular_2016_0 (saved by Fritzing 0.9.3b)
circuit board: 3.7413cm x 5.73205cm
breadboards: 1

parts:
  R2 = Resistor [tolerance=±1% resistance=47k package=THT]
  R1 = Resistor [tolerance=±1% resistance=47k package=THT]
  R3 = Resistor [tolerance=±1% resistance=22k package=THT]
  C1 = Ceramic Capacitor [capacitance=10nF voltage=35V package="100 mil [THT, multilayer]"]
  R4 = Resistor [tolerance=±1% resistance=10k package=THT]
  cutoff = female pin header, 1 pin [form="♀ (female)"]
  mcp4822 = IC, DIP package, 8 pins [chip_label=IC]
  R8 = Resistor [tolerance=±1% resistance=33k package=THT]
  audio = female pin header, 1 pin [form="♀ (female)"]
  pitch = female pin header, 1 pin [form="♀ (female)"]
  C3 = Ceramic Capacitor [capacitance=1µF package="100 mil [THT, multilayer]"]
  R6 = Resistor [tolerance=±1% resistance=2.7k package=THT]
  gate = female pin header, 1 pin [form="♀ (female)"]
  euroPower = shrouded pin header, 10 pins [form="♂ (shrouded male)"]
  C2 = Ceramic Capacitor [capacitance=10nF voltage=35V package="100 mil [THT, multilayer]"]
  R5 = Resistor [tolerance=±1% resistance=22k package=THT]
  GND/+5V = female pin header, 2 pins [form="♀ (female)"]
  LM78L05 = Voltage Regulator [package=to-92]
  C4 = Electrolytic Capacitor [capacitance=10µF voltage=35V package="100 mil [THT, electrolytic]"]
  L1 = Inductor [package="400 mil [THT]"]
  C5 = Ceramic Capacitor [capacitance=100nF package="100 mil [THT, multilayer]"]
  D1 = Schottky Diode [part_number=1N5817 package="300 mil [THT]"]
  Teensy_3_1 = Teensy 3.1

nets:
  N1: R2.Pin_0, Teensy_3_1.D3
  N2: R2.Pin_1, R1.Pin_0, R3.Pin_0
  GND: R1.Pin_1, C1.0, mcp4822.pin5, mcp4822.pin7, euroPower.pin2, euroPower.pin3, euroPower.pin4, euroPower.pin7, euroPower.pin8, euroPower.pin9, C2.0, GND/+5V.pin1, LM78L05.GND, C4.-, C5.1, Teensy_3_1.GND
  N3: R3.Pin_1, C1.1, R4.Pin_0
  N4: R4.Pin_1, cutoff.pin1
  N5: mcp4822.pin1, GND/+5V.pin2, LM78L05.OUT, C5.0, Teensy_3_1.Vin
  N6: mcp4822.pin2, Teensy_3_1.D10
  N7: mcp4822.pin3, Teensy_3_1.D13
  N8: mcp4822.pin4, Teensy_3_1.D11
  N9: mcp4822.pin6, R5.Pin_0
  N10: mcp4822.pin8, C3.0
  N11: R8.Pin_0, C3.1
  N12: R8.Pin_1, audio.pin1
  N13: pitch.pin1, R6.Pin_1
  N14: R6.Pin_0, C2.1, R5.Pin_1
  N15: gate.pin1, Teensy_3_1.D5
  N16: euroPower.pin1, euroPower.pin10
  N17: euroPower.pin5, euroPower.pin6, L1.pin_0
  N18: LM78L05.IN, C4.+, D1.cathode
  N19: L1.pin_1, D1.anode

notes:
  nostromotron
  tr1ptron1c 2016
