# Fritzing sketch id2822_NOT_0 (saved by Fritzing 0.9.2b)
breadboards: 1

parts:
  S1 = Pushbutton [package="[THT]"]
  R1 = Resistor [tolerance=±5% resistance=82 package=THT]
  R2 = Resistor [tolerance=±5% resistance=10k package=THT]
  LED1 = LED - 5mm [color="Red (633nm)" package="5 mm [THT]"]
  Q1 = NPN-Transistor [package="TO92 [THT]"]
  R3 = Resistor [tolerance=±5% resistance=10k package=THT]
  R4 = Resistor [tolerance=±5% resistance=10k package=THT]
  LED2 = LED - 5mm [color="Red (633nm)" package="5 mm [THT]"]
  R5 = Resistor [tolerance=±5% resistance=82 package=THT]

nets:
  N1: S1.Pin_1, S1.Pin_2, R2.Pin_1, LED1.anode, R3.Pin_1
  N2: S1.Pin_3, S1.Pin_4, R4.Pin_1
  GND: R1.Pin_0, R2.Pin_0, Q1.E, R5.Pin_0
  N3: R1.Pin_1, LED1.cathode
  N4: Q1.B, R3.Pin_0
  N5: Q1.C, R4.Pin_0, LED2.anode
  N6: LED2.cathode, R5.Pin_1
