# Fritzing sketch id2823_Zumbador_0 (saved by Fritzing 0.9.3b)
breadboards: 1

parts:
  Componente1 = Arduino Uno (Rev3)
  J1 = Piezo Speaker
  LED1 = LED - 5mm [color="Red (633nm)" package="5 mm [THT]"]
  LED2 = LED - 5mm [color="Red (633nm)" package="5 mm [THT]"]
  R1 = Resistor [tolerance=±5% resistance=220 package=THT]
  R2 = Resistor [tolerance=±5% resistance=220 package=THT]

nets:
  N1: Componente1.D3_PWM, LED2.anode
  N2: Componente1.D4, LED1.anode
  N3: Componente1.D5_PWM, J1.pin2
  N4: Componente1.GND, J1.pin1, R1.Pin_0, R2.Pin_0
  N5: LED1.cathode, R2.Pin_1
  N6: LED2.cathode, R1.Pin_1
