# Fritzing sketch id2824_Shema_0 (saved by Fritzing 0.9.3b)
stripboards: 1

parts:
  RB1 = Resistor [tolerance=±5% resistance=220 package=THT]
  R15 = Resistor [tolerance=±5% resistance=220 package=THT]
  RG2 = Resistor [tolerance=±5% resistance=220 package=THT]
  R_tilt = Resistor [tolerance=±5% resistance=10k package=THT]
  R10 = Resistor [tolerance=±5% resistance=220 package=THT]
  MEGA = Arduino Mega 2560 (Rev3)
  LED11 = LED - 3mm [color="White (4500K)" package="3 mm [THT]"]
  RR1 = Resistor [tolerance=±5% resistance=220 package=THT]
  LED2 = RGB LED - (4 legs) [package="5 mm [THT]"]
  LED6 = RGB LED - (4 legs) [package="5 mm [THT]"]
  RG1 = Resistor [tolerance=±5% resistance=220 package=THT]
  SPR121 = MPR121 Breakout
  LED15 = LED - 3mm [color="White (4500K)" package="3 mm [THT]"]
  LED9 = LED - 3mm [color="White (4500K)" package="3 mm [THT]"]
  LED10 = LED - 3mm [color="White (4500K)" package="3 mm [THT]"]
  RR2 = Resistor [tolerance=±5% resistance=220 package=THT]
  R12 = Resistor [tolerance=±5% resistance=220 package=THT]
  LED5 = RGB LED - (4 legs) [package="5 mm [THT]"]
  R16 = Resistor [tolerance=±5% resistance=220 package=THT]
  R9 = Resistor [tolerance=±5% resistance=220 package=THT]
  LED8 = RGB LED - (4 legs) [package="5 mm [THT]"]
  LED3 = RGB LED - (4 legs) [package="5 mm [THT]"]
  LED16 = LED - 3mm [color="White (4500K)" package="3 mm [THT]"]
  LED12 = LED - 3mm [color="White (4500K)" package="3 mm [THT]"]
  R11 = Resistor [tolerance=±5% resistance=220 package=THT]
  LED1 = RGB LED - (4 legs) [package="5 mm [THT]"]
  R13 = Resistor [tolerance=±5% resistance=220 package=THT]
  LED13 = LED - 3mm [color="White (4500K)" package="3 mm [THT]"]
  LED14 = LED - 3mm [color="White (4500K)" package="3 mm [THT]"]
  R14 = Resistor [tolerance=±5% resistance=220 package=THT]
  LED4 = RGB LED - (4 legs) [package="5 mm [THT]"]
  RB2 = Resistor [tolerance=±5% resistance=220 package=THT]
  LED7 = RGB LED - (4 legs) [package="5 mm [THT]"]
  Réflection_"Tilt" = Tilt Switch [package=THT]

nets:
  N1: RB1.Pin_0, MEGA.D11_PWM
  N2: RB1.Pin_1, LED2.blue_cathode, LED3.blue_cathode, LED1.blue_cathode, LED4.blue_cathode
  N3: R15.Pin_0, LED15.cathode
  GND: R15.Pin_1, R_tilt.Pin_0, R_tilt.Pin_1, R10.Pin_1, MEGA.GND, MEGA.D22, SPR121.GND, R12.Pin_1, R16.Pin_1, R9.Pin_1, R11.Pin_1, R13.Pin_1, R14.Pin_1, Réflection_"Tilt".Pin_2
  N4: RG2.Pin_0, MEGA.D9_PWM
  N5: RG2.Pin_1, LED6.green_cathode, LED5.green_cathode, LED8.green_cathode, LED7.green_cathode
  N6: R10.Pin_0, LED10.cathode
  N7: MEGA.A4, SPR121.SCL
  N8: MEGA.A5, SPR121.SDA
  N9: MEGA.D13_PWM, RR1.Pin_0
  N10: MEGA.D12_PWM, RG1.Pin_0
  N11: MEGA.D10_PWM, RR2.Pin_0
  N12: MEGA.D8_PWM, RB2.Pin_0
  3V3: MEGA.3V3, SPR121.3.3V
  N13: MEGA.5V, LED2.common_anode, LED6.common_anode, LED5.common_anode, LED8.common_anode, LED3.common_anode, LED1.common_anode, LED4.common_anode, LED7.common_anode, Réflection_"Tilt".Pin_1
  N14: MEGA.D2_PWM, LED14.anode
  N15: MEGA.D3_PWM, LED13.anode
  N16: MEGA.D4_PWM, LED12.anode
  N17: MEGA.D5_PWM, LED11.anode
  N18: MEGA.D6_PWM, LED10.anode
  N19: MEGA.D7_PWM, LED9.anode
  N20: MEGA.D44, LED15.anode
  N21: MEGA.D46, LED16.anode
  N22: LED11.cathode, R11.Pin_0
  N23: RR1.Pin_1, LED2.red_cathode, LED3.red_cathode, LED1.red_cathode, LED4.red_cathode
  N24: LED2.green_cathode, RG1.Pin_1, LED3.green_cathode, LED1.green_cathode, LED4.green_cathode
  N25: LED6.red_cathode, RR2.Pin_1, LED5.red_cathode, LED8.red_cathode, LED7.red_cathode
  N26: LED6.blue_cathode, LED5.blue_cathode, LED8.blue_cathode, RB2.Pin_1, LED7.blue_cathode
  N27: LED9.cathode, R9.Pin_0
  N28: R12.Pin_0, LED12.cathode
  N29: R16.Pin_0, LED16.cathode
  N30: R13.Pin_0, LED13.cathode
  N31: LED14.cathode, R14.Pin_0
