# Fritzing sketch id2825_A_type_sensor_node_0 (saved by Fritzing 0.9.2b)
breadboards: 1

parts:
  Part1 = Arduino Pro Mini v13
  DHT1 = DHT22_Humidity_and_Temperature_Sensor
  IC1 = ADS1115_16_bit_ADC_Breakout
  Part2 = OpenLog
  U1 = AVR 10-pin ICSP Header [package=2x5-shrouded_smd]
  R1 = Resistor [tolerance=±5% resistance=10k package=THT]
  C2 = Ceramic Capacitor [capacitance=100nF package="100 mil [THT, multilayer]"]
  C6 = Ceramic Capacitor [capacitance=10nF package="100 mil [THT, multilayer]"]
  Power_plug1 = Power plug

nets:
  N1: Part1.A4, IC1.connector4
  N2: Part1.A5, IC1.connector3
  GND: Part1.GND, Part1.RESET, DHT1.connector4, IC1.connector2, IC1.connector5, Part2.GND, U1.2, C2.1, C6.0, Power_plug1.GND
  VCC: Part1.VCC, Part1.A3, Part1.D13/SCK, DHT1.connector1, IC1.connector1, Part2.VCC, U1.1, R1.Pin_0, C2.0, C6.1, Power_plug1.VCC
  N3: Part1.A0, U1.9
  N4: Part1.D10_PWM/SS, DHT1.connector2, R1.Pin_1
  N5: Part1.D9_PWM, Part2.RXI
  N6: IC1.connector7, U1.6
  N7: IC1.connector8, U1.5
  N8: IC1.connector9, U1.8
  N9: IC1.connector10, U1.7
