# Fritzing sketch id2826_auto_0 (saved by Fritzing 0.9.0b)
breadboards: 1

parts:
  Onderdeel1 = Arduino Uno (Rev3)
  Q1 = NPN-Transistor [package="TO92 [THT]"]

nets:
  N1: Onderdeel1.D2, Q1.E
  N2: Onderdeel1.5V, Q1.C
  GND: Onderdeel1.GND
  12V: Q1.B

notes:
  Car ground
  Car input
