# Fritzing sketch id2827_Transmitter_0 (saved by Fritzing 0.9.3b)
breadboards: 1

parts:
  NRF24L2 = NRF24L01
  Bauteil1 = Arduino Nano (Rev3.0)
  RHT1 = Humidity and Temperature Sensor RHT03

nets:
  N1: NRF24L2.connector0, Bauteil1.3V3
  N2: NRF24L2.connector1, Bauteil1.D8
  N3: NRF24L2.connector2, Bauteil1.D11/MOSI
  N4: NRF24L2.connector4, Bauteil1.GND
  N5: NRF24L2.connector5, Bauteil1.D7
  N6: NRF24L2.connector6, Bauteil1.D13/SCK
  N7: NRF24L2.connector7, Bauteil1.D12/MISO
  N8: Bauteil1.D2, RHT1.Data-signal
  5V: Bauteil1.5V, RHT1.Vcc

notes:
  Suli Project
  Multi RF Transmitter NODE Slave
  pipe nr. pipe01 = 0xE8E8F0F0E1LL;
  DHT 11 Temp.Sensor 5V
  NOTE:
  Stabilization circuit (3.3V) for NRF24L01 are suggested.
