# Fritzing sketch id2828_arduino_nrf24l01_receiver_0 (saved by Fritzing 0.9.2b)
circuit board: 8.46667cm x 5.64444cm
breadboards: 1

parts:
  NRF24L01 = NRF24L01
  Part1 = Arduino Pro Mini v13
  R1 = Resistor [tolerance=±5% resistance=220 package=THT]
  LED1 = LED - 5mm [color="Red (633nm)" package="5 mm [THT]"]

nets:
  N1: NRF24L01.connector0, Part1.VCC
  N2: NRF24L01.connector1, Part1.D10_PWM/SS
  N3: NRF24L01.connector2, Part1.D11_PWM/MOSI
  N4: NRF24L01.connector4, Part1.GND, R1.Pin_1
  N5: NRF24L01.connector5, Part1.D9_PWM
  N6: NRF24L01.connector6, Part1.D13/SCK
  N7: NRF24L01.connector7, Part1.D12/MISO
  N8: Part1.D4, LED1.anode
  N9: R1.Pin_0, LED1.cathode

notes:
  Receiver
  https://anasdalintakam.blogspot.in/
