# Fritzing sketch id2830_ProMini_NRF_v2_0 (saved by Fritzing 0.9.2b)
circuit board: 7cm x 5cm
breadboards: 1

parts:
  Pro_Mini = Arduino Pro Mini v13
  3_3v_Reg = Voltage Regulator -- 3.3 V -- LM1117
  nRF24L01+ = NRF24L01+ Breakout Board
  J7 = female pin header, 3 pins [form="♀ (female)"]
  J8 = female pin header, 3 pins [form="♀ (female)"]
  J9 = female pin header, 3 pins [form="♀ (female)"]
  J10 = female pin header, 3 pins [form="♀ (female)"]
  J12 = female pin header, 3 pins [form="♀ (female)"]
  J14 = rounded female pin header, 13 pins [form="♀ (female rounded)"]  # not connected
  J15 = rounded female pin header, 13 pins [form="♀ (female rounded)"]  # not connected
  J16 = rounded female pin header, 13 pins [form="♀ (female rounded)"]  # not connected
  J17 = rounded female pin header, 13 pins [form="♀ (female rounded)"]  # not connected
  J18 = female pin header, 4 pins [form="♀ (female)"]
  J19 = female pin header, 7 pins [form="♀ (female)"]
  Power_plug1 = Power plug
  J20 = rounded female pin header, 13 pins [form="♀ (female rounded)"]  # not connected
  J21 = female pin header, 3 pins [form="♀ (female)"]
  J2 = rounded female pin header, 15 pins [form="♀ (female rounded)"]  # not connected
  J3 = rounded female pin header, 15 pins [form="♀ (female rounded)"]  # not connected
  J4 = rounded female pin header, 15 pins [form="♀ (female rounded)"]  # not connected
  J5 = rounded female pin header, 15 pins [form="♀ (female rounded)"]  # not connected
  J6 = rounded female pin header, 15 pins [form="♀ (female rounded)"]  # not connected
  10uf = Electrolytic Capacitor [capacitance=10pF voltage=35V package="100 mil [THT, electrolytic]"]
  J1 = rounded female pin header, 10 pins [form="♀ (female rounded)"]  # not connected
  J22 = rounded female pin header, 4 pins [form="♀ (female rounded)"]

nets:
  N1: Pro_Mini.A4, J22.pin4
  N2: Pro_Mini.A5, J22.pin3
  N3: Pro_Mini.RAW, J7.pin1, J8.pin1, J9.pin1, J10.pin1, J12.pin1, Power_plug1.VCC
  GND: Pro_Mini.GND, 3_3v_Reg.connector0, nRF24L01+.GND, J7.pin3, J8.pin3, J9.pin3, J10.pin3, J12.pin3, Power_plug1.GND, 10uf.-
  N4: Pro_Mini.VCC, 3_3v_Reg.connector2, J7.pin2, J8.pin2, J9.pin2, J10.pin2, J12.pin2
  N5: Pro_Mini.A3, J18.pin4
  N6: Pro_Mini.A2, J18.pin3
  N7: Pro_Mini.A1, J18.pin2
  N8: Pro_Mini.A0, J18.pin1
  N9: Pro_Mini.D13/SCK, nRF24L01+.SCK
  N10: Pro_Mini.D12/MISO, nRF24L01+.MISO
  N11: Pro_Mini.D11_PWM/MOSI, nRF24L01+.MOSI
  N12: Pro_Mini.D10_PWM/SS, nRF24L01+.CS
  N13: Pro_Mini.D9_PWM, nRF24L01+.CE
  N14: Pro_Mini.D8, J19.pin1
  N15: Pro_Mini.D7, J19.pin2
  N16: Pro_Mini.D6_PWM, J19.pin3
  N17: Pro_Mini.D5_PWM, J19.pin4
  N18: Pro_Mini.D4, J19.pin5
  N19: Pro_Mini.D3_PWM, J19.pin6
  N20: Pro_Mini.D2, J19.pin7
  N21: 3_3v_Reg.connector1, nRF24L01+.VCC, 10uf.+
  N22: J21.pin1, J22.pin1
  N23: J21.pin2, J22.pin2

notes:
  GND
  7-12v
  A4
  A5
  5v
  A7
  A6
