# Fritzing sketch id2831_NRF52_Arduino_i2c_0 (saved by Fritzing 0.9.3b)
breadboards: 1

parts:
  Part2 = nRF52-DK
  Part3 = Logic Level Converter
  Part4 = Arduino Leonardo (Rev3b)
  R1 = Resistor [tolerance=±5% resistance=220 package="1206 [SMD]"]
  R2 = Resistor [tolerance=±5% resistance=220 package="1206 [SMD]"]
  R3 = Resistor [tolerance=±5% resistance=220 package="1206 [SMD]"]
  R4 = Resistor [tolerance=±5% resistance=220 package="1206 [SMD]"]

nets:
  N1: Part2.connector234, Part3.RX2_LV, R3.Pin_0
  N2: Part2.connector235, Part3.TX2_LV, R4.Pin_0
  N3: Part2.connector257, Part3.LV, R3.Pin_1, R4.Pin_1
  GND: Part2.connector259, Part3.GND, Part4.GND
  N4: Part3.HV, Part4.5V, R1.Pin_0, R2.Pin_0
  N5: Part3.RX2_HV, Part4.SCL, R1.Pin_1
  N6: Part3.TX2_HV, Part4.SDA, R2.Pin_1
