# Fritzing sketch id2833_Nucleotide_Control_RGB_LEDs_0 (saved by Fritzing 0.9.1b)
circuit board: 2.20485cm x 5.82028cm
breadboards: 1

parts:
  R2 = Resistor [tolerance=±5% resistance=8.2k package=THT]
  Q2 = NPN-Transistor [part_number=TIP120 package="TO92 [THT]"]
  R1 = Resistor [tolerance=±5% resistance=8.2k package=THT]
  R3 = Resistor [tolerance=±5% resistance=8.2k package=THT]
  U1 = Voltage Regulator - 5V [part_number=LM2940CT-5.0 package="TO220 [THT]"]
  LED1 = RGB LED (com. cathode, rgb) [part_number="12V RGB LED strip(s)" package="5 mm [THT]"]
  Q1 = NPN-Transistor [part_number=TIP120 package="TO92 [THT]"]
  Q3 = NPN-Transistor [part_number=TIP120 package="TO92 [THT]"]
  Part1 = Arduino Pro Mini v13 [part_number=Atmega328P]
  C2 = Electrolytic Capacitor [capacitance=1µF voltage=50V package="100 mil [THT, electrolytic]"]
  C1 = Electrolytic Capacitor [capacitance=22µF voltage=50V package="100 mil [THT, electrolytic]"]

nets:
  N1: R2.Pin_0, Part1.D5_PWM
  N2: R2.Pin_1, Q2.B
  GND: Q2.E, U1.GND, Q1.E, Q3.E, Part1.GND, C2.-, C1.-
  N3: Q2.C, LED1.blue_anode
  N4: R1.Pin_0, Part1.D6_PWM
  N5: R1.Pin_1, Q1.B
  N6: R3.Pin_0, Part1.D3_PWM
  N7: R3.Pin_1, Q3.B
  12V: U1.input_voltage, LED1.common_cathode, C2.+
  N8: U1.output_voltage, Part1.VCC, C1.+
  N9: LED1.red_anode, Q1.C
  N10: LED1.green_anode, Q3.C

notes:
  Circuit to go with the Nucleotide-Control-RGB-LEDs code
  12V DC is provided by a recycled GameCube power brick
