# Fritzing sketch id2834_number_game_0 (saved by Fritzing 0.9.0b)
breadboards: 1

parts:
  S1 = Pushbutton [package="[THT]"]
  S2 = Pushbutton [package="[THT]"]
  Part1 = Arduino Uno (Rev3)
  7_Segment2 = 7 Segment Display
  LED1 = LED - 5mm [color="Red (633nm)" package="5 mm [THT]"]
  LED2 = LED - 5mm [color="Red (633nm)" package="5 mm [THT]"]
  7_Segment3 = 7 Segment Display
  R4 = Resistor [tolerance=±5% resistance=220 package=THT]
  R1 = Resistor [tolerance=±5% resistance=10k package=THT]
  R2 = Resistor [tolerance=±5% resistance=10k package=THT]
  R3 = Resistor [tolerance=±5% resistance=220 package=THT]

nets:
  N1: S1.Pin_1, S1.Pin_2, S2.Pin_3, S2.Pin_4, Part1.5V
  N2: S1.Pin_3, S1.Pin_4, Part1.D12/MISO, R1.Pin_1
  N3: S2.Pin_1, S2.Pin_2, Part1.D13/SCK, R2.Pin_0
  N4: Part1.A0, LED1.anode
  N5: Part1.A1, 7_Segment2.Segment_B
  N6: Part1.A2, 7_Segment3.Segment_G
  N7: Part1.A3, 7_Segment3.Segment_F
  N8: Part1.A4/SDA, 7_Segment3.Segment_A
  N9: Part1.A5/SCL, 7_Segment3.Segment_B
  N10: Part1.D8, LED2.anode
  N11: Part1.D9_PWM, 7_Segment3.Segment_E
  N12: Part1.D10_PWM/SS, 7_Segment3.Segment_D
  N13: Part1.D11_PWM/MOSI, 7_Segment3.Segment_C
  N14: Part1.D2, 7_Segment2.Segment_A
  N15: Part1.D3_PWM, 7_Segment2.Segment_F
  N16: Part1.D4, 7_Segment2.Segment_G
  N17: Part1.D5_PWM, 7_Segment2.Segment_E
  N18: Part1.D6_PWM, 7_Segment2.Segment_D
  N19: Part1.D7, 7_Segment2.Segment_C
  N20: Part1.GND, 7_Segment2.common_anode, 7_Segment3.common_anode, R4.Pin_1, R1.Pin_0, R2.Pin_1, R3.Pin_1
  N21: LED1.cathode, R4.Pin_0
  N22: LED2.cathode, R3.Pin_0
