# Fritzing sketch id2835_nw_0 (saved by Fritzing 0.9.2b)
breadboards: 1

parts:
  R1 = Resistor [tolerance=±5% resistance=220 package=THT]
  VCC1 = Battery
  LED1 = LED - 5mm [color="Red (633nm)" package="5 mm [THT]"]  # not connected
  LED2 = LED - 5mm [color="Red (633nm)" package="5 mm [THT]"]
  S1 = Round Pushbutton
  R2 = Resistor [tolerance=±5% resistance=220 package=THT]

nets:
  N1: R1.Pin_0, VCC1.+, S1.leg0, S1.leg1
  N2: R1.Pin_1, R2.Pin_0
  N3: VCC1.-, LED2.anode
  N4: LED2.cathode, R2.Pin_1
