# Fritzing sketch id2838_obi_sketch_1_0 (saved by Fritzing 0.9.2b)
breadboards: 1

parts:
  Part1 = Arduino Uno (Rev3)
  M1 = DC Motor
  IC2 = L293D [package=THT]
  S1 = Pushbutton [package="[THT]"]
  S2 = Pushbutton [package="[THT]"]
  S3 = Toggle Switch [package=THT]
  VCC1 = Battery
  U1 = 2.4GHz Low Power Transceiver [package=qfn20]
  R1 = Resistor [tolerance=±5% resistance=220 package=THT]

nets:
  N1: Part1.A0, R1.Pin_0
  N2: Part1.D8, U1.SCK
  N3: Part1.D9_PWM, IC2.Enable_1
  N4: Part1.D11_PWM/MOSI, U1.IRQ
  N5: Part1.D12/MISO, U1.VDD
  N6: Part1.D13/SCK, U1.MISO
  N7: Part1.D2, S3.COM
  N8: Part1.D3_PWM, IC2.In_2, S1.Pin_3, S1.Pin_4
  N9: Part1.D4, IC2.In_1, S2.Pin_3, S2.Pin_4
  N10: Part1.D5_PWM, M1.pin_2, IC2.Out_2_(_Controlled_by_Enable_1_)
  N11: Part1.D7, U1.MOSI
  N12: Part1.3V3, U1.CSN
  N13: Part1.5V, IC2.+V, S3.L2
  N14: Part1.GND, IC2.0V, S3.L1, VCC1.-, U1.CE
  N15: IC2.Out_1_(_Controlled_by_Enable_1_), R1.Pin_1
  N16: IC2.+Vmotor, VCC1.+
  N17: S1.Pin_1, S1.Pin_2
  N18: S2.Pin_1, S2.Pin_2
