# Fritzing sketch id283_completeAlarmClock_0 (saved by Fritzing 0.8.7b)
circuit board: 11.1cm x 5.8cm
circuit board: 5.5cm x 2.1cm
circuit board: 10.6cm x 6.5cm
breadboards: 6

parts:
  ATMega168 = atmega168 [package=dip]
  10K = Resistor [tolerance=±20% resistance=10k package=THT]
  16MHz = Crystal [frequency="16 Mhz" package=THT]
  22pF = Ceramic Capacitor [capacitance=100nF package="100 mil [THT, multilayer]"]
  22pF_2 = Ceramic Capacitor [capacitance=10pF package="100 mil [THT, multilayer]"]
  H11AA1 = Optocoupler [package=THT]
  Tilt_Sw = Tilt Switch [package=THT]
  B3 = Pushbutton [package="[THT]"]
  B2 = Pushbutton [package="[THT]"]
  B1 = Pushbutton [package="[THT]"]
  10K_2 = Resistor [tolerance=±5% resistance=10k package=THT]
  10K_3 = Resistor [tolerance=±5% resistance=10k package=THT]
  10K_4 = Resistor [tolerance=±5% resistance=10k package=THT]
  10K_5 = Resistor [tolerance=±5% resistance=10k package=THT]
  10K_6 = Resistor [tolerance=±20% resistance=10k package=THT]
  MAX72XX = MAX7219 [package=dil24]
  100nF = Ceramic Capacitor [capacitance=100nF package="100 mil [THT, multilayer]"]
  ACDC_Converter = ACDCConverter
  Speaker = SPEAKER [package=pcb_mount_speaker]
  B4 = Pushbutton [package="[THT]"]
  RGB_LED = RGB LED (com. anode, rbg) [package="5 mm [THT]"]
  470R = Resistor [tolerance=±5% resistance=470 package=THT]
  470R_2 = Resistor [tolerance=±5% resistance=470 package=THT]
  470R_3 = Resistor [tolerance=±5% resistance=470 package=THT]
  Pot_meter = TRIMPOT [package=trimpot_pth_s3_lock]
  Main_Reg = Voltage Regulator - 5V [package="TO220 [THT]"]
  10uF = Electrolytic Capacitor [capacitance=10µF package="100 mil [THT, electrolytic]"]
  10uF_2 = Electrolytic Capacitor [capacitance=10µF package="100 mil [THT, electrolytic]"]
  ATMega_Slave = atmega168 [package=dip]
  16MHz_2 = Crystal [frequency="16 Mhz" package=THT]
  22pF_3 = Ceramic Capacitor [capacitance=100nF package="100 mil [THT, multilayer]"]
  22pF_4 = Ceramic Capacitor [capacitance=100nF package="100 mil [THT, multilayer]"]
  10K_7 = Resistor [tolerance=±5% resistance=10k package=THT]
  Sound_Reg = Voltage Regulator - 5V [package="TO220 [THT]"]
  100uF = Electrolytic Capacitor [capacitance=10µF package="100 mil [THT, electrolytic]"]
  220K = Resistor [tolerance=±5% resistance=470k package=THT]
  7_segment_4_digit_LED = 7-SEGMENT-4DIGIT-12-PINS
  Sound_Card = WTV020-SD-mini
  Fuse = Low-amperage-fuse
  Relay = Fujitsu-Power-Relay
  Coil = AC-induction-coil
  MOC3031 = MOC3031-M [package=dil06]
  30K_Ohm_1/2_W = AC-resistor-with-wider-soldering-points
  30K_Ohm_1/2_W_2 = AC-resistor-with-wider-soldering-points
  220R = Resistor [tolerance=±5% resistance=220 package=THT]
  10K_8 = Resistor [tolerance=±20% resistance=10k package=THT]
  1_7K = AC-resistor-with-wider-soldering-points
  470_Ohm = AC-resistor-with-wider-soldering-points
  5_6K = Resistor [tolerance=±5% resistance=10k package=THT]
  10uF_3 = Electrolytic Capacitor [capacitance=10µF package="100 mil [THT, electrolytic]"]
  22R = Resistor [tolerance=±5% resistance=22 package=THT]
  TRIAC = Voltage Regulator [part_number="This is actually a TRIAC" package=to220-adj]
  RTC = Tiny-DS1307-RTC-Time-Module
  100nF_2 = AC-Capacitor-3382MKP
  Mains = Header with larger soldering points
  Lamp = Header with larger soldering points

nets:
  N1: ATMega168.RESET, 10K.Pin_1
  N2: ATMega168.D2, Sound_Card.connector0
  N3: ATMega168.D3_(PWM), 470R.Pin_0
  N4: ATMega168.D4, Sound_Card.connector6
  VCC: ATMega168.VCC, ATMega168.AVCC, ATMega168.AREF, 10K.Pin_0, B3.Pin_1, B3.Pin_2, B2.Pin_1, B2.Pin_2, B1.Pin_1, B1.Pin_2, MAX72XX.VCC, 100nF.1, B4.Pin_1, B4.Pin_2, Main_Reg.output_voltage, 10uF_2.-, ATMega_Slave.VCC, ATMega_Slave.AVCC, ATMega_Slave.AREF, 10K_7.Pin_1, 100uF.+, 220K.Pin_1, 10K_8.Pin_0, 5_6K.Pin_0, RTC.connector2
  GND: ATMega168.GND, 22pF.0, 22pF_2.0, H11AA1.Pin_4, 10K_2.Pin_0, 10K_3.Pin_0, 10K_4.Pin_0, 10K_5.Pin_0, 10K_6.Pin_1, MAX72XX.GND, MAX72XX.GND2, 100nF.0, ACDC_Converter.connector2, RGB_LED.common_anode, Pot_meter.CW, Main_Reg.GND, 10uF.+, 10uF_2.+, ATMega_Slave.GND, 22pF_3.1, 22pF_4.1, Sound_Reg.GND, 100uF.-, Sound_Card.connector7, Relay.connector2, MOC3031.2, 10uF_3.+, RTC.connector3
  N5: ATMega168.XLAT1, 16MHz.pin_0, 22pF.1
  N6: ATMega168.XLAT2, 16MHz.pin_1, 22pF_2.1
  N7: ATMega168.D5_(PWM), 470R_2.Pin_0
  N8: ATMega168.D6_(PWM), 470R_3.Pin_0
  N9: ATMega168.D7, Sound_Card.connector9
  N10: ATMega168.D8, Sound_Card.connector14
  N11: ATMega168.D9_(PWM), Tilt_Sw.Pin_2, 10K_6.Pin_0
  N12: ATMega168.D10_(PWM), MAX72XX.LOAD
  N13: ATMega168.D11_(PWM), MAX72XX.CLK
  N14: ATMega168.D12, MAX72XX.DIN
  N15: ATMega168.A0, B1.Pin_3, B1.Pin_4, 10K_2.Pin_1
  N16: ATMega168.A1, B2.Pin_3, B2.Pin_4, 10K_3.Pin_1
  N17: ATMega168.A2, B3.Pin_3, B3.Pin_4, 10K_4.Pin_1
  N18: ATMega168.A3, 10K_5.Pin_1, B4.Pin_3, B4.Pin_4
  N19: ATMega168.A4, ATMega_Slave.A4, RTC.connector1
  N20: ATMega168.A5, ATMega_Slave.A5, RTC.connector0
  N21: H11AA1.Pin_1, 30K_Ohm_1/2_W.connector1
  N22: H11AA1.Pin_2, 30K_Ohm_1/2_W_2.connector1
  N23: H11AA1.Pin_5, ATMega_Slave.D2, 10K_8.Pin_1
  N24: Tilt_Sw.Pin_1, 5_6K.Pin_1
  N25: MAX72XX.DIG0, 7_segment_4_digit_LED.connector14
  N26: MAX72XX.DIG2, 7_segment_4_digit_LED.connector10
  N27: MAX72XX.DIG3, 7_segment_4_digit_LED.connector6
  N28: MAX72XX.DIG1, 7_segment_4_digit_LED.connector11
  N29: MAX72XX.SEGA, 7_segment_4_digit_LED.connector13
  N30: MAX72XX.SEGF, 7_segment_4_digit_LED.connector12
  N31: MAX72XX.SEGB, 7_segment_4_digit_LED.connector9
  N32: MAX72XX.SEGG, 7_segment_4_digit_LED.connector5
  N33: MAX72XX.ISET, 220K.Pin_0
  N34: MAX72XX.SEGC, 7_segment_4_digit_LED.connector4
  N35: MAX72XX.SEGE, 7_segment_4_digit_LED.connector1
  N36: MAX72XX.SEGDP, 7_segment_4_digit_LED.connector3
  N37: MAX72XX.SEGD, 7_segment_4_digit_LED.connector2
  N38: ACDC_Converter.connector0, 30K_Ohm_1/2_W_2.connector0, Mains.connector1, Lamp.connector0
  N39: ACDC_Converter.connector1, Relay.connector4, Mains.connector0
  N40: ACDC_Converter.connector3, Fuse.connector2
  N41: Speaker.+, Pot_meter.WIPER
  N42: Speaker.-, Sound_Card.connector4
  N43: RGB_LED.red_cathode, 470R.Pin_1
  N44: RGB_LED.blue_cathode, 470R_2.Pin_1
  N45: RGB_LED.green_cathode, 470R_3.Pin_1
  N46: Pot_meter.CCW, Sound_Card.connector3
  N47: Main_Reg.input_voltage, 10uF.-, Sound_Reg.input_voltage, Fuse.connector0
  N48: ATMega_Slave.RESET, 10K_7.Pin_0
  N49: ATMega_Slave.D4, 220R.Pin_1
  N50: ATMega_Slave.XLAT1, 16MHz_2.pin_1, 22pF_4.0
  N51: ATMega_Slave.XLAT2, 16MHz_2.pin_0, 22pF_3.0
  N52: ATMega_Slave.D7, 22R.Pin_1
  N53: Sound_Reg.output_voltage, Sound_Card.connector15, 10uF_3.-
  N54: Relay.connector1, 30K_Ohm_1/2_W.connector0, 1_7K.connector1, 470_Ohm.connector1, TRIAC.IN
  N55: Relay.connector3, 22R.Pin_0
  N56: Coil.connector0, 100nF_2.connector0, Lamp.connector1
  N57: Coil.connector1, TRIAC.ADJ
  N58: MOC3031.1, 220R.Pin_0
  N59: MOC3031.4, TRIAC.OUT
  N60: MOC3031.6, 1_7K.connector0
  N61: 470_Ohm.connector0, 100nF_2.connector1
  N62: RTC.connector6, RTC.connector14

notes:
  +ve
  -ve
  A5
  A4
  Reset
  CLK
  BUSY
  Data
  speaker -
  speaker +
