# Fritzing sketch id2841_CONTADOR_0 (saved by Fritzing 0.9.2b)
breadboards: 2

parts:
  Parte1 = Arduino Uno (Rev3)
  R1 = Resistor [tolerance=±5% resistance=220 package=THT]
  LED1 = LED - 5mm [color="Red (633nm)" package="5 mm [THT]"]
  CONTADOR_01 = LCD screen
  LED3 = LED - 5mm [color="Green (570nm)" package="5 mm [THT]"]
  LED4 = LED - 5mm [color="Green (570nm)" package="5 mm [THT]"]
  R2 = Resistor [tolerance=±5% resistance=220 package=THT]
  R3 = Resistor [tolerance=±5% resistance=330 package=THT]
  R4 = Resistor [tolerance=±5% resistance=330 package=THT]
  R5 = Resistor [tolerance=±5% resistance=220 package=THT]
  LED5 = LED - 5mm [color="Infrared (880nm)" package="5 mm [THT]"]
  LED6 = LED - 5mm [color="Infrared (880nm)" package="5 mm [THT]"]
  R6 = Resistor [tolerance=±5% resistance=220 package=THT]
  R7 = Resistor [tolerance=±5% resistance=220 package=THT]
  U1 = ENCODER-QUADRATURE [package=encoder-16mm-quad]

nets:
  N1: Parte1.D10_PWM/SS, LED1.anode
  N2: Parte1.D11_PWM/MOSI, CONTADOR_01.E
  N3: Parte1.D12/MISO, CONTADOR_01.RS
  N4: Parte1.D2, CONTADOR_01.DB7
  N5: Parte1.D3_PWM, CONTADOR_01.DB6
  N6: Parte1.D4, CONTADOR_01.DB5
  N7: Parte1.D5_PWM, CONTADOR_01.DB4
  N8: Parte1.D6_PWM, LED4.cathode, R4.Pin_0
  N9: Parte1.D7, LED3.cathode, R3.Pin_0
  5V: Parte1.5V, CONTADOR_01.VDD, CONTADOR_01.LED+, R2.Pin_1, R5.Pin_1, R6.Pin_0, R7.Pin_0, U1.C
  GND: Parte1.GND, R1.Pin_1, CONTADOR_01.VSS, CONTADOR_01.R/W, CONTADOR_01.LED-, R3.Pin_1, R4.Pin_1, LED5.cathode, LED6.cathode, U1.A
  N10: R1.Pin_0, LED1.cathode
  N11: CONTADOR_01.V0, U1.B
  N12: LED3.anode, R2.Pin_0
  N13: LED4.anode, R5.Pin_0
  N14: LED5.anode, R6.Pin_1
  N15: LED6.anode, R7.Pin_1
