# Fritzing sketch id2842_board_0 (saved by Fritzing 0.8.7b)
breadboards: 1

parts:
  Part1 = Arduino Uno (Rev3)
  LED1 = LED - 5mm [color="Red (633nm)" package="5 mm [THT]"]
  R1 = Resistor [tolerance=±5% resistance=220 package=THT]
  R2 = Resistor [tolerance=±5% resistance=220 package=THT]
  LED2 = LED - 5mm [color="Yellow (595nm)" package="5 mm [THT]"]
  R3 = Resistor [tolerance=±5% resistance=220 package=THT]
  LED3 = LED - 5mm [color="Green (570nm)" package="5 mm [THT]"]
  R4 = Resistor [tolerance=±5% resistance=220 package=THT]
  LED4 = LED - 5mm [color="Red (633nm)" package="5 mm [THT]"]
  R5 = Resistor [tolerance=±5% resistance=220 package=THT]
  LED5 = LED - 5mm [color="Green (560nm)" package="5 mm [THT]"]
  S1 = Pushbutton [package="[THT]"]
  R6 = Resistor [tolerance=±5% resistance=220 package=THT]

nets:
  N1: Part1.D8, S1.Pin_1, S1.Pin_2, R6.Pin_1
  N2: Part1.D9_PWM, R5.Pin_0
  N3: Part1.D10_PWM/SS, R4.Pin_0
  N4: Part1.D11_PWM/MOSI, R3.Pin_0
  N5: Part1.D12/MISO, R2.Pin_0
  N6: Part1.D13/SCK, R1.Pin_0
  N7: Part1.GND, LED1.anode, LED2.anode, LED3.anode, LED4.anode, LED5.anode, R6.Pin_0
  N8: Part1.5V, S1.Pin_3, S1.Pin_4
  N9: LED1.cathode, R1.Pin_1
  N10: R2.Pin_1, LED2.cathode
  N11: R3.Pin_1, LED3.cathode
  N12: R4.Pin_1, LED4.cathode
  N13: R5.Pin_1, LED5.cathode
