# Fritzing sketch id2843_obstacleAvoidanceRobot_0 (saved by Fritzing 0.9.3b)

parts:
  IC2 = H-Bridge [package=THT]
  Part1 = Arduino Mega 2560 (Rev3)
  M1 = DC Motor
  M2 = DC Motor
  hc-sr1 = hc-sr04
  J1 = Basic Servo
  VCC2 = Battery block 9V

nets:
  N1: IC2.1_2EN, Part1.D45
  N2: IC2.1A, Part1.D30
  N3: IC2.1Y, M2.pin_2
  GND1: IC2.GND1, IC2.GND2
  N4: IC2.2Y, M2.pin_1
  N5: IC2.2A, Part1.D31
  N6: IC2.3_4EN, Part1.D44
  N7: IC2.3A, Part1.D28
  N8: IC2.3Y, M1.pin_2
  GND3: IC2.GND3, IC2.GND4, VCC2.-
  N9: IC2.4Y, M1.pin_1
  N10: IC2.4A, Part1.D29
  N11: IC2.VCC1, VCC2.+
  GND: Part1.GND, hc-sr1.GND
  N12: Part1.D9_PWM, J1.pulse
  VCC: Part1.5V, hc-sr1.VCC, J1.vcc
  N13: Part1.D2_PWM, hc-sr1.Echo
  N14: Part1.D3_PWM, hc-sr1.Trig
