# Fritzing sketch id2844_oar_0 (saved by Fritzing 0.9.3b)
breadboards: 1

parts:
  Part1 = Arduino Uno (Rev3) - ICSP
  S1 = Ponte-H L298N
  M1 = DC Motor  # not connected
  M2 = DC Motor
  J1 = Basic Servo
  hc-sr1 = hc-sr04
  VCC2 = Battery block 9V  # not connected
  VCC3 = Battery block 9V

nets:
  N1: Part1.A1, hc-sr1.Trig
  N2: Part1.A2, hc-sr1.Echo
  VCC: Part1.5V, J1.vcc, hc-sr1.VCC
  N3: Part1.D10_PWM/SS, J1.pulse
  N4: Part1.D4, S1.connector6
  N5: Part1.D5_PWM, S1.connector5
  N6: Part1.D6_PWM, S1.connector4
  N7: Part1.D7, S1.connector3
  GND: Part1.GND, S1.connector1, J1.gnd, hc-sr1.GND
  N8: S1.connector0, VCC3.+
  N9: S1.connector7, M2.pin_1
  N10: S1.connector8, M2.pin_2
