# Fritzing sketch id2846_sound_meter_0 (saved by Fritzing 0.9.3b)

parts:
  Part1 = Arduino Pro Mini (5V)
  Part2 = Breakout Board for Electret Microphone [part_number=MAX4466]
  S1 = Toggle Switch [package=THT]
  S2 = Toggle Switch [package=THT]
  SP1 = SPEAKER [package=pcb_mount_speaker]
  U1 = LCD-16X2 [package=lcd-8x2]
  LED1 = smd LED [color="Red (633nm)" package="0603 [SMD]"]
  LED2 = smd LED [color="Orange (620nm)" package="0603 [SMD]"]
  LED3 = smd LED [color="Green (555nm)" package="0603 [SMD]"]
  LED4 = smd LED [color="Blue (470nm)" package="0603 [SMD]"]
  R2 = Resistor [tolerance=±5% resistance=220 package=THT]
  R3 = Resistor [tolerance=±5% resistance=220 package=THT]
  R4 = Resistor [tolerance=±5% resistance=220 package=THT]
  R5 = Resistor [tolerance=±5% resistance=220 package=THT]
  VCC2 = Battery block 9V
  VCC3 = Battery block 9V
  KY-5 = keyes
  Part3 = Arduino Pro Mini (5V)
  Part4 = Breakout Board for Electret Microphone [part_number=MAX4466]
  S3 = Toggle Switch [package=THT]
  VCC4 = Battery block 9V
  J1 = Piezo Speaker
  LED5 = RGB LED (com. anode, rbg) [package="5 mm [THT]"]
  U2 = LCD-16X2 [package=lcd-8x2]

nets:
  N1: Part1.RAW, S1.COM
  GND: Part1.GND, Part2.GND, VCC3.-, KY-5.connector2
  VCC: Part1.VCC, Part2.VCC, KY-5.connector1
  N2: Part1.A0, Part2.AUD
  N3: Part1.MISO, U1.DB5
  N4: Part1.MOSI, U1.DB3
  N5: Part1.D10, U1.DB1
  N6: Part1.D9, U1.E
  N7: Part1.D8, U1.RS
  N8: Part1.D7, U1.VDD
  N9: Part1.D6, KY-5.connector0
  N10: Part1.D5, R5.Pin_1
  N11: Part1.D4, R3.Pin_1
  N12: Part1.D3, R2.Pin_1
  N13: Part1.D2, R4.Pin_1
  N14: Part1.RESET, LED1.cathode, LED2.cathode, LED3.cathode, LED4.cathode
  N15: S1.L1, VCC3.+
  N16: S2.L1, KY-5.connector4
  N17: S2.COM, VCC2.+
  N18: SP1.+, VCC2.-
  N19: SP1.-, KY-5.connector5
  N20: Part3.RAW, S3.COM
  GND_2: Part3.GND, Part4.GND, VCC4.-, J1.pin1, LED5.common_anode
  VCC_2: Part3.VCC, Part4.VCC
  N21: Part3.A1, J1.pin2
  N22: Part3.A0, Part4.AUD
  N23: Part3.MISO, U2.K
  N24: Part3.MOSI, U2.DB7
  N25: Part3.D10, U2.DB5
  N26: Part3.D9, U2.E
  N27: Part3.D8, U2.RS
  N28: Part3.D7, U2.VDD
  N29: Part3.D4, LED5.red_cathode
  N30: Part3.D3, LED5.blue_cathode
  N31: Part3.D2, LED5.green_cathode
  N32: S3.L1, VCC4.+
