# Fritzing sketch id2847_Office_status_0 (saved by Fritzing 0.9.2b)

parts:
  Part1 = adafruit [part_number="Adafruit #2821"]  # not connected
  Part2 = adafruit [part_number=258]

nets:
  N1: Part2.connector1, Part2.connector2

notes:
  Lämpliga resistorer till resp LED utelämnade i figuren
