# Fritzing sketch id2848_RL_first_sketch_0 (saved by Fritzing 0.9.3b)
breadboards: 1

parts:
  R1 = Resistor [tolerance=±5% resistance=220 package=THT]
  LED1 = LED - 5mm [color="Red (633nm)" package="5 mm [THT]"]
  VCC1 = Battery
  R2 = Resistor [tolerance=±5% resistance=220 package=THT]  # not connected

nets:
  N1: R1.Pin_0, VCC1.+
  N2: LED1.anode, VCC1.-
