# Fritzing sketch id2849_Untitled_Sketch_0 (saved by Fritzing 0.9.2b)
breadboards: 1

parts:
  Componente1 = Arduino Uno (Rev3)
  R1 = Resistor [tolerance=±5% resistance=330 package=THT]
  LED1 = LED - 5mm [color="Red (633nm)" package="5 mm [THT]"]
  R2 = Resistor [tolerance=±5% resistance=10k package=THT]
  LED2 = RGB LED (com. cathode, rgb) [package="5 mm [THT]"]
  S1 = Pushbutton [package=THT]
  R3 = Resistor [tolerance=±5% resistance=330 package=THT]
  R4 = Resistor [tolerance=±5% resistance=330 package=THT]
  R5 = Resistor [tolerance=±5% resistance=330 package=THT]

nets:
  N1: Componente1.D2, R2.Pin_0, S1.leg1
  N2: Componente1.D3_PWM, R4.Pin_0
  N3: Componente1.D4, R3.Pin_0
  N4: Componente1.D5_PWM, R5.Pin_0
  N5: Componente1.D6_PWM, R1.Pin_0
  N6: Componente1.GND, LED1.anode, R2.Pin_1, LED2.common_cathode
  N7: R1.Pin_1, LED1.cathode
  N8: LED2.red_anode, R5.Pin_1
  N9: LED2.green_anode, R3.Pin_1
  N10: LED2.blue_anode, R4.Pin_1

notes:
  Sketch do Arduino
