# Fritzing sketch id284_ALARMA_LASER_0 (saved by Fritzing 0.8.7b)
breadboards: 1

parts:
  SENSOR_DE_LUZ = Arduino Uno (Rev3)
  INTERRUPTOR = Pushbutton [package=THT]
  RESISTENCIA = Resistor [tolerance=±5% resistance=1k package=THT]
  LDR = Photocell (LDR) [package=THT]
  POTENCIOMETRO = Rotary Potentiometer (Small) [maximum_resistance=10kΩ package=THT]
  RESISTENCIA_2 = Resistor [tolerance=±5% resistance=1k package=THT]
  BOCINA = Piezo Speaker

nets:
  N1: SENSOR_DE_LUZ.A0, LDR.pin_0, RESISTENCIA_2.Pin_1
  N2: SENSOR_DE_LUZ.D8, INTERRUPTOR.leg0, RESISTENCIA.Pin_0
  N3: SENSOR_DE_LUZ.D12/MISO, BOCINA.pin2
  N4: SENSOR_DE_LUZ.GND, RESISTENCIA.Pin_1, POTENCIOMETRO.leg1, RESISTENCIA_2.Pin_0, BOCINA.pin1
  N5: SENSOR_DE_LUZ.AREF, POTENCIOMETRO.wiper
  N6: SENSOR_DE_LUZ.5V, INTERRUPTOR.leg1, LDR.pin_1, POTENCIOMETRO.leg2
