# Fritzing sketch id2851_helloworld_0 (saved by Fritzing 0.9.3b)
circuit board: 8.46667cm x 5.64444cm
breadboards: 1

parts:
  LED1 = LED - 5mm [color="Red (633nm)" package="5 mm [THT]"]
  R1 = Resistor [tolerance=±5% resistance=330 package=THT]
  Componente1 = Arduino Uno (Rev3)

nets:
  N1: LED1.cathode, Componente1.GND
  N2: LED1.anode, R1.Pin_0
  N3: R1.Pin_1, Componente1.D13/SCK
