# Fritzing sketch id2852_OLED_und_DHT22_0 (saved by Fritzing 0.9.3b)
breadboards: 1

parts:
  Raspberry_Pi_1 = Raspberry Pi 3 [part_number=RPI-3-V1.2]
  RHT1 = Humidity and Temperature Sensor RHT03
  R1 = Resistor [tolerance=±5% resistance=10k package=THT]
  OLED_I2C1 = OLED 128x64 I2C Monochrome Display

nets:
  3V3: Raspberry_Pi_1.3v3, RHT1.Vcc, R1.Pin_1, OLED_I2C1.connector7
  N1: Raspberry_Pi_1.GPIO2, OLED_I2C1.connector4
  N2: Raspberry_Pi_1.GPIO3, OLED_I2C1.connector5
  N3: Raspberry_Pi_1.GPIO21, RHT1.Data-signal, R1.Pin_0
  N4: Raspberry_Pi_1.GND, RHT1.GND_2, OLED_I2C1.connector8
