# Fritzing sketch id2854_7805_variable_fan_regulator_0 (saved by Fritzing 0.8.3b)
breadboards: 1

parts:
  R1 = Trimmer Potentiometer [maximum_resistance=1kΩ package=THT]
  R2 = Resistor [tolerance=±5% resistance=1k package=THT]
  C1 = Ceramic Capacitor [capacitance=100nF voltage=16V package="100 mil [THT, multilayer]"]
  U1 = Voltage Regulator - 5V [package="TO220 [THT]"]
  J2 = male pin header, 3 pins [form="♂ (male)"]
  C2 = Ceramic Capacitor [capacitance=100nF voltage=16V package="100 mil [THT, multilayer]"]
  J1 = male pin header, 3 pins [form="♂ (male)"]

nets:
  N1: R1.wiper, R2.Pin_1, U1.GND
  N2: R1.leg2, C1.0, J2.pin2, C2.0, J1.pin2
  N3: R2.Pin_0, C1.1, U1.output_voltage, J2.pin1
  N4: U1.input_voltage, C2.1, J1.pin1
  N5: J2.pin3, J1.pin3

notes:
  Vin = 12V (red)
  Vout = variable (red)
  RPM sensor in (yellow)
  0V (black)
  RPM sensor out (yellow)
  7805 variable fan regulator
