# Fritzing sketch id2855_fritz_twoPushBtn_oneNeoPixelRing_0 (saved by Fritzing 0.9.3b)
circuit board: 8.46667cm x 5.64444cm
breadboards: 1

parts:
  Part1 = Arduino Uno (Rev3)
  S1 = Pushbutton [package="[THT]"]
  Part2 = adafruit [part_number=1643]
  S2 = Pushbutton [package="[THT]"]

nets:
  N1: Part1.D8, S2.Pin_3, S2.Pin_4
  N2: Part1.D9_PWM, S1.Pin_1, S1.Pin_2
  N3: Part1.GND, S1.Pin_3, S1.Pin_4, Part2.connector20, S2.Pin_1, S2.Pin_2
  N4: Part1.D5_PWM, Part2.connector17
  N5: Part1.5V, Part2.connector19
