# Fritzing sketch id2857_KP_oneWire_Passcode_0 (saved by Fritzing 0.9.2b)
breadboards: 1

parts:
  Bauteil1 = Arduino Uno (Rev3)
  R1 = Resistor [tolerance=±5% resistance=1k package=THT]
  R2 = Resistor [tolerance=±5% resistance=1k package=THT]
  R3 = Resistor [tolerance=±5% resistance=1k package=THT]
  R4 = Resistor [tolerance=±5% resistance=4.7k package=THT]
  R5 = Resistor [tolerance=±5% resistance=4.7k package=THT]
  R6 = Resistor [tolerance=±5% resistance=4.7k package=THT]
  Matrix_keypad1 = CMG
  R7 = Resistor [tolerance=±5% resistance=1k package=THT]
  LCM1602_IIC1 = generic_ic_dip_22_300mil.fzp [part_number="LCM1602 IIC" chip_label="LCM1602 IIC"]
  LCD1 = LCD screen  # not connected
  LED1 = LED - 3mm [color="Red (633nm)" package="3 mm [THT]"]
  LED2 = LED - 3mm [color="Green (555nm)" package="3 mm [THT]"]
  R8 = Resistor [tolerance=±5% resistance=220 package=THT]
  R9 = Resistor [tolerance=±5% resistance=220 package=THT]
  J1 = Basic Servo

nets:
  N1: Bauteil1.A0, R1.Pin_0, Matrix_keypad1.connector29, R7.Pin_1
  N2: Bauteil1.A4/SDA, LCM1602_IIC1.connector18
  N3: Bauteil1.A5/SCL, LCM1602_IIC1.connector19
  N4: Bauteil1.D8, J1.pulse
  N5: Bauteil1.D12/MISO, LED2.anode
  N6: Bauteil1.D13/SCK, LED1.anode
  GND: Bauteil1.GND, R7.Pin_0, LCM1602_IIC1.connector16, R8.Pin_0, R9.Pin_0, J1.gnd
  5V: Bauteil1.5V, R6.Pin_0, Matrix_keypad1.connector25, LCM1602_IIC1.connector17, J1.vcc
  N7: R1.Pin_1, R2.Pin_0, Matrix_keypad1.connector30
  N8: R2.Pin_1, R3.Pin_0, Matrix_keypad1.connector31
  N9: R3.Pin_1, Matrix_keypad1.connector32
  N10: R4.Pin_0, R5.Pin_1, Matrix_keypad1.connector27
  N11: R4.Pin_1, Matrix_keypad1.connector28
  N12: R5.Pin_0, R6.Pin_1, Matrix_keypad1.connector26
  N13: LED1.cathode, R9.Pin_1
  N14: LED2.cathode, R8.Pin_1

notes:
  LCD 16x02 with I2C
  4x 1KOhm
  3x 4,7 KOhm
  2x 220 Ohm
