# Fritzing sketch id2858_OnlineThermometer_0 (saved by Fritzing 0.9.2b)
breadboards: 1

parts:
  Part1 = Arduino Yun
  DHT2 = DHT11_Temperature_and_Humitidy_Sensor
  R1 = Resistor [tolerance=±5% resistance=4.7k package=THT]

nets:
  N1: Part1.5V, DHT2.connector1, R1.Pin_0
  N2: Part1.GND, DHT2.connector4
  N3: Part1.D2, DHT2.connector2, R1.Pin_1
