# Fritzing sketch id2859_CountDownSwitch_0 (saved by Fritzing 0.4.3b)
breadboards: 1

parts:
  U1000 = PkS-01
  S1111 = Pushbutton [package="[THT]"]
  S1112 = Pushbutton [package="[THT]"]
  R1121 = Resistor [resistance=220 package=THT]
  R1221 = Resistor [resistance=220 package=THT]
  VCC1 = Battery block 9V
  Side1 = Paper_A3_Horizontal
  LED1113 = Red LED-R - 3mm
  LED1114 = Red LED-R - 3mm
  LED1115 = Yellow LED-R - 3mm
  LED1116 = Yellow LED-R - 3mm
  LED1117 = Yellow LED-R - 3mm
  LED1118 = Yellow LED-R - 3mm
  LED1119 = Green LED-R - 3mm
  LED1120 = Green LED-R - 3mm
  LED1105 = Red LED-R - 3mm
  LED1106 = Green LED-R - 3mm

nets:
  N1: U1000.connector4, LED1105.connector1
  N2: U1000.connector5, LED1106.connector1
  N3: U1000.connector10, S1111.Pin_1, S1111.Pin_2, R1221.Pin_1
  N4: U1000.connector11, S1112.Pin_1, S1112.Pin_2, R1121.Pin_1
  N5: U1000.connector12, LED1113.connector1
  N6: U1000.connector13, LED1114.connector1
  N7: U1000.connector14, LED1115.connector1
  N8: U1000.connector15, LED1116.connector1
  N9: U1000.connector16, LED1117.connector1
  N10: U1000.connector17, LED1118.connector1
  N11: U1000.connector18, LED1119.connector1
  N12: U1000.connector19, LED1120.connector1
  N13: U1000.connector20, R1121.Pin_0, R1221.Pin_0
  N14: U1000.connector22, S1111.Pin_3, S1111.Pin_4, S1112.Pin_3, S1112.Pin_4, VCC1.-, Side1.connector0, LED1113.connector0, LED1114.connector0, LED1115.connector0, LED1116.connector0, LED1117.connector0, LED1118.connector0, LED1119.connector0, LED1120.connector0, LED1105.connector0, LED1106.connector0
  N15: U1000.connector23, VCC1.+

notes:
  On/Off Count Down Switch
  Reference Project of PROFESSIONALkitStamp
  mjf / 19.10.2010
  1/1
  05.09.2009
  On
  Off
  switching output
  Inverted
  switching output
