# Fritzing sketch id2863_OP_AMP_Audio_Amplifier_0 (saved by Fritzing 0.5.2b)
breadboards: 1

parts:
  IC1 = IC, DIP package, 8 pins [chip_label=KA4558 spacing=300mil]
  TRS1 = Stereo Jack (TRS) 3.5mm [package="PG203J [THT]"]
  J1 = female pin header, 7 pins [form="♀ (female)"]
  R1 = Rotary Potentiometer (Small)
  SPKR1 = Loudspeaker
  VCC1 = Battery block 9V

nets:
  N1: IC1.pin1, TRS1.Ring, J1.pin3
  N2: IC1.pin2, IC1.pin4, SPKR1.pin1
  N3: IC1.pin3, J1.pin6, R1.leg2
  N4: IC1.pin5, TRS1.Tip, J1.pin4
  N5: IC1.pin6, IC1.pin8, TRS1.Sleeve, J1.pin1, J1.pin2, VCC1.-, VCC1.+
  N6: IC1.pin7, J1.pin5, R1.leg1
  N7: J1.pin7, R1.wiper, SPKR1.pin2

notes:
  [OUTPUT-------------------------------------------------------------------------------INPUT]
  PINS OF HEADER Left:Right
  [1-9v ] [2-GND] [3-IN,1] [4-IN2] [5-OUT2] [6-OUT1]
  [7BAL_TONE_OUT((1-2))]
  HEADER-\/
