# Fritzing sketch id2864_op_amp_0 (saved by Fritzing 0.8.5b)
breadboards: 1

parts:
  Part1 = Arduino Uno (Rev3)
  TRS1 = Audio Jack (TRS) 3.5mm [package="PG203J [THT]"]
  R1 = Resistor [tolerance=±5% resistance=10k package=THT]
  R2 = Resistor [tolerance=±5% resistance=10k package=THT]
  U1 = LM 358 Dual Op-Amp [package="DIP8 [THT]"]
  R3 = Resistor [tolerance=±5% resistance=10k package=THT]
  R4 = Resistor [tolerance=±20% resistance=100k package=THT]
  R5 = Resistor [tolerance=±5% resistance=120 package=THT]
  C1 = Electrolytic Capacitor [capacitance=10µF package="1010 [SMD, electrolytic]"]
  LED1 = LED - 5mm [color="Red (633nm)" package="5 mm [THT]"]
  R6 = Resistor [tolerance=±5% resistance=220 package=THT]
  RGB_SMD_LED1 = SMD RGB LED (WS2812) [package=5050]

nets:
  N1: Part1.A0, R5.Pin_1, C1.+
  N2: Part1.D13/SCK, LED1.anode
  GND: Part1.GND, TRS1.Sleeve, U1.connector3, R3.Pin_1, C1.-, R6.Pin_0, RGB_SMD_LED1.VSS
  N3: Part1.D6_PWM, RGB_SMD_LED1.DIn
  5V: Part1.5V, U1.connector7, RGB_SMD_LED1.VCC
  N4: TRS1.Ring, R2.Pin_0
  N5: TRS1.Tip, R1.Pin_0
  N6: R1.Pin_1, U1.connector2
  N7: U1.connector0, R4.Pin_1, R5.Pin_0
  N8: U1.connector1, R3.Pin_0, R4.Pin_0
  N9: LED1.cathode, R6.Pin_1
