# Fritzing sketch id2865_montage_V4_JNL_0 (saved by Fritzing 0.9.2b)
breadboards: 1

parts:
  U2 = MIC [package=mic-9.7mm]
  U3 = LM 358 Dual Op-Amp [package="DIP8 [THT]"]
  R20 = Resistor [tolerance=±5% resistance=1M package="0805 [SMD]"]
  R21 = Resistor [tolerance=±5% resistance=3.3k package="0805 [SMD]"]
  R24 = Resistor [tolerance=±5% resistance=10k package="0805 [SMD]"]
  C2 = Electrolytic Capacitor [capacitance=100µF package="0405 [SMD, electrolytic]"]
  U4 = LM 358 Dual Op-Amp [package="DIP8 [THT]"]
  SP1 = SPEAKER [package=pcb_mount_speaker]
  U14 = LM 358 Dual Op-Amp [package="DIP8 [THT]"]
  R29 = Resistor [tolerance=±5% resistance=220 package=THT]
  R30 = Resistor [tolerance=±5% resistance=220 package=THT]
  C9 = Electrolytic Capacitor [capacitance=1µF package="100 mil [THT, electrolytic]"]
  C10 = Electrolytic Capacitor [capacitance=100µF package="0405 [SMD, electrolytic]"]
  R31 = Resistor [tolerance=±5% resistance=82 package="0805 [SMD]"]
  C11 = Tantalum Capacitor [capacitance=100nF package="100 mil [THT, tantalum]"]
  C12 = Tantalum Capacitor [capacitance=100nF package="100 mil [THT, tantalum]"]
  C13 = Capacitor Polarized [package=panasonic_c]
  R33 = Resistor [tolerance=±5% resistance=100k package="0805 [SMD]"]
  R34 = Resistor [tolerance=±5% resistance=100k package="0805 [SMD]"]
  V15 = DC Power [voltage=3V]
  R35 = Resistor [tolerance=±5% resistance=220 package=THT]
  R36 = Resistor [tolerance=±5% resistance=220 package=THT]
  C14 = Electrolytic Capacitor [capacitance=1µF package="100 mil [THT, electrolytic]"]
  R37 = Resistor [tolerance=±5% resistance=220 package=THT]
  R38 = Resistor [tolerance=±5% resistance=220 package=THT]
  C15 = Electrolytic Capacitor [capacitance=1µF package="100 mil [THT, electrolytic]"]
  C16 = Electrolytic Capacitor [capacitance=1µF package="100 mil [THT, electrolytic]"]
  U20 = LM 358 Dual Op-Amp [package="DIP8 [THT]"]
  R39 = Resistor [tolerance=±5% resistance=220 package=THT]
  R40 = Resistor [tolerance=±5% resistance=220 package=THT]
  R41 = Resistor [tolerance=±5% resistance=220 package=THT]
  R42 = Resistor [tolerance=±5% resistance=220 package=THT]
  R43 = Resistor [tolerance=±5% resistance=220 package=THT]
  R44 = Resistor [tolerance=±5% resistance=390 package=THT]
  R45 = Resistor [tolerance=±10% resistance=3.2k package=THT]
  U17 = LM 358 Dual Op-Amp [package="DIP8 [THT]"]
  U19 = LM 358 Dual Op-Amp [package="DIP8 [THT]"]

nets:
  GND: U2.1, U3.connector2, C2.-, SP1.-, R29.Pin_0, C9.-, C11.-, R35.Pin_0, R43.Pin_1, R44.Pin_1, U19.connector2
  N1: U2.2, R24.Pin_1, C10.+
  N2: U3.connector0, R20.Pin_1, U4.connector2
  N3: U3.connector1, R20.Pin_0, R21.Pin_1
  -1.5V: U3.connector3, U4.connector3, U14.connector3, C13.-, R33.Pin_1, V15.V-, U20.connector3, U17.connector3, U19.connector3
  N4: U3.connector5, U3.connector6, R31.Pin_0
  1.5V: U3.connector7, U4.connector7, U14.connector7, R34.Pin_0, V15.V+, U20.connector7, U17.connector7, U19.connector7
  N5: R21.Pin_0, C10.-
  3.3V: R24.Pin_0, C2.+
  N6: U4.connector0, U4.connector1, R37.Pin_0, R45.Pin_1
  N7: U4.connector4, R31.Pin_1
  N8: U4.connector5, U4.connector6, C11.+, C12.-
  N9: SP1.+, U20.connector5, U20.connector6
  N10: U14.connector0, R30.Pin_1, R40.Pin_0
  N11: U14.connector1, R29.Pin_1, R30.Pin_0
  N12: U14.connector2, C9.+, R45.Pin_0
  0V: C13.+, R33.Pin_0, R34.Pin_1
  N13: R35.Pin_1, R36.Pin_0, U17.connector1
  N14: R36.Pin_1, U17.connector0, U17.connector4
  N15: C14.-, R44.Pin_0, U17.connector2
  N16: R37.Pin_1, C15.+
  N17: R38.Pin_0, C15.-, C16.+, U19.connector1
  N18: R38.Pin_1, C16.-, R41.Pin_0
  N19: U20.connector0, U20.connector4, R42.Pin_1
  N20: U20.connector1, R39.Pin_1, R40.Pin_1, R41.Pin_1
  N21: U20.connector2, R42.Pin_0, R43.Pin_0
  N22: R39.Pin_0, U17.connector5, U17.connector6
  N23: U19.connector5, U19.connector6

notes:
  Passe bas avec gain
  gain :  (R29+R30)/R29
  fc = 1/(2*pi*R*C)
  Passe haut avec gain
  gain :  (R25+R36)/R25
  Alimentation Symetrique a partir de la pile
  Passe bande avec gain
  res et condo non dimentionné
  res non dimentionné
