# Fritzing sketch id2867_5Button_IRQ_Keypad (saved by Fritzing 0.6.3b)
breadboards: 1

parts:
  S1 = Pushbutton [package="[THT]"]
  S2 = Pushbutton [package="[THT]"]
  S3 = Pushbutton [package="[THT]"]
  S4 = Pushbutton [package="[THT]"]
  S5 = Pushbutton [package="[THT]"]
  D1 = Rectifier Diode [part_number=1N4007 package="300 mil [THT]"]
  D2 = Rectifier Diode [part_number=1N4007 package="300 mil [THT]"]
  D3 = Rectifier Diode [part_number=1N4007 package="300 mil [THT]"]
  D4 = Rectifier Diode [part_number=1N4007 package="300 mil [THT]"]
  D5 = Rectifier Diode [part_number=1N4007 package="300 mil [THT]"]
  R1 = Resistor [tolerance=±5% resistance=220 package=THT]
  R2 = Resistor [tolerance=±5% resistance=220 package=THT]
  R3 = Resistor [tolerance=±5% resistance=220 package=THT]
  R4 = Resistor [tolerance=±5% resistance=220 package=THT]
  R5 = Resistor [tolerance=±5% resistance=220 package=THT]
  LED1 = LED - 5mm [color="Green (555nm)" package="5 mm [THT]"]
  LED2 = LED - 5mm [color="Green (555nm)" package="5 mm [THT]"]
  LED3 = LED - 5mm [color="Green (555nm)" package="5 mm [THT]"]
  LED4 = LED - 5mm [color="Green (555nm)" package="5 mm [THT]"]
  LED5 = LED - 5mm [color="Green (555nm)" package="5 mm [THT]"]
  R6 = Resistor [tolerance=±5% resistance=10k package=THT]
  Arduino1 = Arduino
  NXP_HEF_4067BP1 = NXP_4067BP [part_number="NXP HEF 4067BP"]

nets:
  N1: S1.Pin_1, S1.Pin_2, D2.anode, NXP_HEF_4067BP1.connector2
  N2: S1.Pin_3, S1.Pin_4, S2.Pin_3, S2.Pin_4, S3.Pin_3, S3.Pin_4, S4.Pin_3, S4.Pin_4, S5.Pin_3, S5.Pin_4, Arduino1.+5V, NXP_HEF_4067BP1.connector23
  N3: S2.Pin_1, S2.Pin_2, D4.anode, NXP_HEF_4067BP1.connector22
  N4: S3.Pin_1, S3.Pin_2, D3.anode, NXP_HEF_4067BP1.connector1
  N5: S4.Pin_1, S4.Pin_2, D5.anode, NXP_HEF_4067BP1.connector21
  N6: S5.Pin_1, S5.Pin_2, D1.anode, NXP_HEF_4067BP1.connector3
  N7: D1.cathode, D2.cathode, D3.cathode, D4.cathode, D5.cathode, R6.Pin_0, Arduino1.D2
  N8: R1.Pin_0, LED1.cathode
  N9: R1.Pin_1, R2.Pin_1, R3.Pin_1, R4.Pin_1, R5.Pin_1, R6.Pin_1, Arduino1.GND, NXP_HEF_4067BP1.connector11, NXP_HEF_4067BP1.connector14, NXP_HEF_4067BP1.connector15, NXP_HEF_4067BP1.connector16, NXP_HEF_4067BP1.connector17, NXP_HEF_4067BP1.connector18, NXP_HEF_4067BP1.connector19, NXP_HEF_4067BP1.connector20
  N10: R2.Pin_0, LED2.cathode
  N11: R3.Pin_0, LED3.cathode
  N12: R4.Pin_0, LED4.cathode
  N13: R5.Pin_0, LED5.cathode
  N14: LED1.anode, NXP_HEF_4067BP1.connector8
  N15: LED2.anode, NXP_HEF_4067BP1.connector7
  N16: LED3.anode, NXP_HEF_4067BP1.connector6
  N17: LED4.anode, NXP_HEF_4067BP1.connector5
  N18: LED5.anode, NXP_HEF_4067BP1.connector4
  N19: Arduino1.D8, NXP_HEF_4067BP1.connector0
  N20: Arduino1.D7, NXP_HEF_4067BP1.connector12
  N21: Arduino1.D6, NXP_HEF_4067BP1.connector13
  N22: Arduino1.D5, NXP_HEF_4067BP1.connector10
  N23: Arduino1.D4, NXP_HEF_4067BP1.connector9

notes:
  Grey wire Pin 8 goes to the common i/o pin of the 4067 De/Multiplexer
  the orange lanes from the arduino are the adress lanes
  the violet lane is the interrupt lane and leads to the breadboard row with the 10k resistor
  the red wires from the 4067 controll the 5 leds. the 5 yellow lanes are for the button-states.
  the adresses for the leds:
  0-4
  and for the buttons:
  5-9
