# Fritzing sketch id2868_Opto_Interrupter_Circuit_0 (saved by Fritzing 0.9.2b)
breadboards: 1

parts:
  R1 = Resistor [tolerance=±5% resistance=330 package=THT]
  R2 = Resistor [tolerance=±5% resistance=2.2k package=THT]
  U1 = CNZ1120 [package=cnz1120]

nets (from the schematic view):
  5V: R1.Pin_0, R2.Pin_1
  N1: R1.Pin_1, U1.1
  N2: R2.Pin_0, U1.3
  GND: U1.2, U1.4

notes:
  Red
  Black
  Green
  White
  You read off the White wire ( the collector )
  Since it is tied to the VCC it is normally High. When there is a break in the beam the line goes Low.
