# Fritzing sketch id286_alarma_0 (saved by Fritzing 0.9.3b)
breadboards: 1

parts:
  Raspberry_Pi_1 = Raspberry Pi 3 [part_number=RPI-3-V1.2]
  J1 = Piezo Speaker
  R1 = Resistor [tolerance=±5% resistance=220 package="2010 [SMD]"]
  LED1 = LED - 5mm [color="Red (633nm)" package="5 mm [THT]"]

nets:
  N1: Raspberry_Pi_1.GPIO26, J1.pin2, LED1.anode
  N2: Raspberry_Pi_1.GND, J1.pin1, R1.Pin_0
  N3: R1.Pin_1, LED1.cathode
