# Fritzing sketch id2870_Opto_Isolator2_0 (saved by Fritzing 0.9.2b)
circuit board: 8.46667cm x 5.64444cm
breadboards: 1

parts:
  R1 = Resistor [tolerance=±5% resistance=1.5k package=THT]
  J1 = female pin header, 2 pins [form="♀ (female)"]
  C2 = Ceramic Capacitor [capacitance=100nF package="100 mil [THT, multilayer]"]
  J2 = female pin header, 2 pins [form="♀ (female)"]
  D1 = Schottky Diode [part_number=1N5817 package="300 mil [THT]"]
  C1 = Ceramic Capacitor [capacitance=1nF voltage=20V package="100 mil [THT, multilayer]"]
  R3 = Resistor [tolerance=±5% resistance=1k package=THT]
  U1 = 817_optocoupler

nets:
  N1: R1.Pin_0, J1.pin1
  N2: R1.Pin_1, D1.cathode, C1.1, U1.connector0
  N3: J1.pin2, D1.anode, C1.0, U1.connector1
  5V/GND: C2.0, C2.1, J2.pin2, R3.Pin_0, U1.connector2
  N4: J2.pin1, R3.Pin_1, U1.connector3

notes:
  Opto-isolator Circuit
  Sharp 817 opto-coupler, 5kHz rated
  Reverse protection diode is shottky with 20V or higher rating (1N5817 is 20V peak, 1A part)
  Input capacitor C1 should be 20V rated or higher
  Input LED forward voltage ~1.2V typ at 10mA forward current
  100kHz noise cutoff using input RC Low Pass filter, with 3us rise time
  Input current limit resistor is 0.25W 1.5k resistor
  1.5k delivers
  ~7mA from 12V,
  ~5mA max at rated input voltage
  ~4mA at low input of 7V
  max power 100mW in input resistor at max voltage
  Input threshold approx 2.5mA with 1k load resistor
  A smaller input resistor can be used to raise the frequency repsonse (see datasheet)
  Designed for inputs of between 7V and 12 V, 9V nominal
  Output resistor allows for full output low voltage at >5mA output current
  0.1uF Vcc decoupling required close to Vcc and GND pins
  For connection to Raspberry Pi use a level converter to convert from 5V logic to 3.3V.
  Input 7V to 12V, 9V nominal, 5kHz
  Note that grounds are not joined between source and circuit.
  Example use:
  simple opto isolator
  This work by hobbyistdave is licensed under a Creative Commons Attribution-ShareAlike 4.0 International License
  No warranty either express or implied is given.
  This schematic was created with Fritzing.
