# Fritzing sketch id2872_os21_temp_humidity_0 (saved by Fritzing 0.9.3b)
circuit board: 2.69935cm x 4.45706cm
breadboards: 1

parts:
  Part3 = Arduino Nano (Rev3.0)
  RHT2 = Humidity and Temperature Sensor RHT03
  433 = female pin header, 3 pins [form="♀ (female)"]
  +1 = Battery
  R4 = Resistor [tolerance=±5% resistance=220 package=THT]

nets:
  N1: Part3.D2, RHT2.Data-signal, R4.Pin_1
  N2: Part3.D9, 433.pin1
  VIN: Part3.VIN, Part3.5V, RHT2.Vcc, 433.pin2, +1.-, R4.Pin_0
  N3: Part3.GND, RHT2.GND_2, 433.pin3, +1.+
