# Fritzing sketch id2873_OrganoLuces_0 (saved by Fritzing 0.7.7b)
breadboards: 1

parts:
  IC1 = IC, DIP package, 8 pins [chip_label=u741]
  C1 = Electrolytic Capacitor [capacitance=4.7µF package="100 mil [THT, electrolytic]"]
  R1 = Resistor [tolerance=±5% resistance=27k package=THT]
  R2 = Resistor [tolerance=±5% resistance=2.7k package=THT]
  R3 = Resistor [tolerance=±5% resistance=270k package=THT]
  R4 = Resistor [tolerance=±5% resistance=6.8k package=THT]  # not connected
  R5 = Resistor [tolerance=±5% resistance=6.8k package=THT]
  Parte1 = Breakout Board for Electret Microphone [part_number="SKU: 135533"]
  C2 = Ceramic Capacitor [capacitance=220nF package="100 mil [THT, multilayer]"]
  R6 = Resistor [tolerance=±5% resistance=1k package=THT]
  Arduino1 = Arduino
  LED1 = LED - 5mm [color="Blue (470nm)" package="5 mm [THT]"]
  LED2 = LED - 5mm [color="Green (555nm)" package="5 mm [THT]"]
  LED3 = LED - 5mm [color="Red (633nm)" package="5 mm [THT]"]
  R7 = Resistor [tolerance=±5% resistance=150 package=THT]
  R8 = Resistor [tolerance=±5% resistance=150 package=THT]
  R9 = Resistor [tolerance=±5% resistance=150 package=THT]

nets:
  N1: IC1.pin2, R3.Pin_0, C2.1
  N2: IC1.pin3, R5.Pin_0
  GND: IC1.pin4, R2.Pin_1, Parte1.GND, Arduino1.GND, LED1.cathode, LED2.cathode, LED3.cathode
  N3: IC1.pin6, C1.-, R3.Pin_1
  N4: IC1.pin7, R1.Pin_0, R5.Pin_1, R6.Pin_1, Arduino1.+5V
  N5: C1.+, R1.Pin_1, R2.Pin_0, Arduino1.A0
  N6: Parte1.VCC, R6.Pin_0
  N7: Parte1.AUD, C2.0
  N8: Arduino1.D11, R9.Pin_1
  N9: Arduino1.D10, R8.Pin_1
  N10: Arduino1.D9, R7.Pin_1
  N11: LED1.anode, R9.Pin_0
  N12: LED2.anode, R8.Pin_0
  N13: LED3.anode, R7.Pin_0

notes:
  SKU: 135533
  + : 5V
  G : Masa
  AO: Salida analógica
  DO: Salida digital
