# Fritzing sketch id2874_oscilador_cristal_0 (saved by Fritzing 0.8.7b)
breadboards: 1

parts:
  R1 = Resistor [tolerance=±5% resistance=1k package=THT]
  C1 = Ceramic Capacitor [capacitance=100pF package="100 mil [THT, multilayer]"]
  C2 = Ceramic Capacitor [capacitance=100pF package="100 mil [THT, multilayer]"]
  R2 = Resistor [tolerance=±5% resistance=22k package=THT]
  C3 = Ceramic Capacitor [capacitance=100nF package="100 mil [THT, multilayer]"]
  C4 = Ceramic Capacitor [capacitance=1nF package="100 mil [THT, multilayer]"]
  ANT1 = Antenna
  VCC1 = Battery block 9V
  XTAL1 = Crystal [frequency="8 MHz" package=THT]
  Q1 = NPN-Transistor [part_number=BC584 package="TO92 [THT]"]

nets:
  N1: R1.Pin_0, C1.0, C2.1, C4.0, Q1.E
  N2: R1.Pin_1, C3.0, VCC1.+, XTAL1.pin_1
  N3: C1.1, R2.Pin_1
  N4: R2.Pin_0, C3.1, VCC1.-, Q1.C
  N5: C4.1, ANT1.antenna_lead
  N6: XTAL1.pin_0, Q1.B

notes:
  Oscilador a cristal
