# Fritzing sketch id2875_progetto_220v_0 (saved by Fritzing 0.9.2b)
circuit board: 11.6258cm x 5.06876cm
breadboards: 1

parts:
  IC2 = General purpose bipolar Timer [part_number=ir2153 package=dil-08]
  U1 = DIODE-ZENER [package=diode-zener]
  Componente1 = Variable Capacitor [capacitance=100nF max_capacitance=10pF min_capacitance=2pF voltage=35V]
  part = Resistor [tolerance=±5% resistance=10k package=THT]
  C2 = Ceramic Capacitor [capacitance=300pF voltage=35V package="200 mil [THT, multilayer]"]
  C1 = Tantalum Capacitor [capacitance=1µF package="200 mil [THT, tantalum]"]
  C3 = Tantalum Capacitor [capacitance=1µF package="200 mil [THT, tantalum]"]
  C4 = Tantalum Capacitor [capacitance=1μF package="100 mil [THT, tantalum]"]
  R1 = Resistor [tolerance=±5% resistance=220 package=THT]
  Q1 = Basic FET N-Channel [package="TO220 [THT]"]
  R2 = Resistor [tolerance=±5% resistance=220 package=THT]
  Q2 = Basic FET N-Channel [package="TO220 [THT]"]
  D1 = Rectifier Diode [part_number=1N4001 package="300 mil [THT]"]
  D2 = Rectifier Diode [part_number=1N4001 package="300 mil [THT]"]
  C5 = Ceramic Capacitor [capacitance=100nF package="200 mil [THT, multilayer]"]
  C6 = Ceramic Capacitor [capacitance=100nF package="200 mil [THT, multilayer]"]
  R3 = Resistor [tolerance=±5% resistance=220 package=THT]
  C7 = Ceramic Capacitor [capacitance=100nF package="200 mil [THT, multilayer]"]

nets:
  N1: IC2.GND, U1.A, C1.+
  N2: IC2.TRI, Componente1.1
  N3: IC2.OUT, part.Pin_1
  N4: IC2._RES, C2.0
  N5: IC2.CON, R2.Pin_0
  N6: IC2.TRE, C4.-, Q1.source, Q2.drain, D1.anode, D2.anode, R3.Pin_0
  N7: IC2.DIS, R1.Pin_0
  N8: IC2.VCC+, U1.C, C4.+
  N9: Componente1.0, part.Pin_0
  N10: C2.1, C1.-, C3.-, Q2.source, D2.cathode, C6.1
  N11: C3.+, Q1.drain, D1.cathode, C5.1
  N12: R1.Pin_1, Q1.gate
  N13: R2.Pin_1, Q2.gate
  N14: C5.0, C6.0, C7.0
  N15: R3.Pin_1, C7.1
