# Fritzing sketch id2876_Osiloskop_0 (saved by Fritzing 0.9.1b)
breadboards: 1

parts:
  C1 = Ceramic Capacitor [capacitance=100nF package="100 mil [THT, multilayer]"]
  C2 = Ceramic Capacitor [capacitance=100nF package="100 mil [THT, multilayer]"]
  Eleman1 = Arduino Uno (Rev3)
  R1 = Resistor [package="2010 [SMD]"]
  R2 = Resistor [package="2010 [SMD]"]

nets:
  N1: C1.0, C2.0, Eleman1.GND, R1.Pin_0, R2.Pin_1
  N2: C1.1, Eleman1.D5_PWM, R2.Pin_0
  N3: C2.1, Eleman1.D6_PWM, R1.Pin_1

notes:
  Osiloskop'un X girişine bağlıyoruz.
  Osiloskop'un Y girişine bağlıyoruz.
  www.eymenalpat.blogspot.com.tr
