# Fritzing sketch id2877_MotorDiagram_0 (saved by Fritzing 0.9.3b)

parts:
  U2 = L298 [package=multiwatt15_6400bgheatsink]
  Part1 = Arduino Uno (Rev3)
  M1 = DC Motor
  M2 = DC Motor
  M3 = DC Motor
  M4 = DC Motor

nets:
  N1: U2.CSA, Part1.5V
  N2: U2.OUT1, M1.pin_1, M2.pin_1
  N3: U2.OUT2, M1.pin_2, M2.pin_2
  N4: U2.IN1, Part1.D11_PWM/MOSI
  N5: U2.IN2, Part1.D10_PWM/SS
  GND: U2.GND, Part1.GND
  N6: U2.IN3, Part1.D6_PWM
  N7: U2.IN4, Part1.D5_PWM
  N8: U2.OUT3, M3.pin_1, M4.pin_1
  N9: U2.OUT4, M3.pin_2, M4.pin_2
  N10: U2.CSB, Part1.VIN
