# Fritzing sketch id2878_ouija001_0 (saved by Fritzing 0.9.3b)
breadboards: 2

parts:
  Composant1 = Arduino Mega 2560 (Rev3)
  LED3 = LED - 5mm [color="Yellow (595nm)" package="5 mm [THT]"]
  LED4 = LED - 5mm [color="Yellow (595nm)" package="5 mm [THT]"]
  LED6 = LED - 5mm [color="Yellow (595nm)" package="5 mm [THT]"]
  LED7 = LED - 5mm [color="Yellow (595nm)" package="5 mm [THT]"]
  R1 = Resistor [tolerance=±5% resistance=220 package=THT]
  R2 = Resistor [tolerance=±5% resistance=220 package=THT]
  R3 = Resistor [tolerance=±5% resistance=220 package=THT]
  R4 = Resistor [tolerance=±5% resistance=220 package=THT]
  LED8 = LED - 5mm [color="Yellow (595nm)" package="5 mm [THT]"]
  LED9 = LED - 5mm [color="Yellow (595nm)" package="5 mm [THT]"]
  LED10 = LED - 5mm [color="Yellow (595nm)" package="5 mm [THT]"]
  LED11 = LED - 5mm [color="Yellow (595nm)" package="5 mm [THT]"]
  R5 = Resistor [tolerance=±5% resistance=220 package=THT]
  R6 = Resistor [tolerance=±5% resistance=220 package=THT]
  R7 = Resistor [tolerance=±5% resistance=220 package=THT]
  R8 = Resistor [tolerance=±5% resistance=220 package=THT]
  LED12 = LED - 5mm [color="Yellow (595nm)" package="5 mm [THT]"]
  LED13 = LED - 5mm [color="Yellow (595nm)" package="5 mm [THT]"]
  LED14 = LED - 5mm [color="Yellow (595nm)" package="5 mm [THT]"]
  LED15 = LED - 5mm [color="Yellow (595nm)" package="5 mm [THT]"]
  LED16 = LED - 5mm [color="Yellow (595nm)" package="5 mm [THT]"]
  LED17 = LED - 5mm [color="Yellow (595nm)" package="5 mm [THT]"]
  LED18 = LED - 5mm [color="Yellow (595nm)" package="5 mm [THT]"]
  LED19 = LED - 5mm [color="Yellow (595nm)" package="5 mm [THT]"]
  R9 = Resistor [tolerance=±5% resistance=220 package=THT]
  R10 = Resistor [tolerance=±5% resistance=220 package=THT]
  R11 = Resistor [tolerance=±5% resistance=220 package=THT]
  R12 = Resistor [tolerance=±5% resistance=220 package=THT]
  R13 = Resistor [tolerance=±5% resistance=220 package=THT]
  R14 = Resistor [tolerance=±5% resistance=220 package=THT]
  R15 = Resistor [tolerance=±5% resistance=220 package=THT]
  R16 = Resistor [tolerance=±5% resistance=220 package=THT]
  LED22 = LED - 5mm [color="Yellow (595nm)" package="5 mm [THT]"]
  LED23 = LED - 5mm [color="Yellow (595nm)" package="5 mm [THT]"]
  LED24 = LED - 5mm [color="Yellow (595nm)" package="5 mm [THT]"]
  LED27 = LED - 5mm [color="Yellow (595nm)" package="5 mm [THT]"]
  R17 = Resistor [tolerance=±5% resistance=220 package=THT]
  R21 = Resistor [tolerance=±5% resistance=220 package=THT]
  R22 = Resistor [tolerance=±5% resistance=220 package=THT]
  R23 = Resistor [tolerance=±5% resistance=220 package=THT]
  LED28 = LED - 5mm [color="Yellow (595nm)" package="5 mm [THT]"]
  LED29 = LED - 5mm [color="Yellow (595nm)" package="5 mm [THT]"]
  LED34 = LED - 5mm [color="Yellow (595nm)" package="5 mm [THT]"]
  LED38 = LED - 5mm [color="Yellow (595nm)" package="5 mm [THT]"]
  LED41 = LED - 5mm [color="Yellow (595nm)" package="5 mm [THT]"]
  LED42 = LED - 5mm [color="Yellow (595nm)" package="5 mm [THT]"]
  R29 = Resistor [tolerance=±5% resistance=220 package=THT]
  R30 = Resistor [tolerance=±5% resistance=220 package=THT]
  R31 = Resistor [tolerance=±5% resistance=220 package=THT]
  R32 = Resistor [tolerance=±5% resistance=220 package=THT]
  R33 = Resistor [tolerance=±5% resistance=220 package=THT]
  R35 = Resistor [tolerance=±5% resistance=220 package=THT]
  J1 = Screw terminal - 2 pins [package=THT]
  J2 = Screw terminal - 2 pins [package=THT]
  J3 = Screw terminal - 2 pins [package=THT]
  J4 = Screw terminal - 2 pins [package=THT]
  J5 = Screw terminal - 2 pins [package=THT]
  J6 = Screw terminal - 2 pins [package=THT]
  J7 = Screw terminal - 2 pins [package=THT]
  J8 = Screw terminal - 2 pins [package=THT]
  J9 = Screw terminal - 2 pins [package=THT]
  J10 = Screw terminal - 2 pins [package=THT]
  J11 = Screw terminal - 2 pins [package=THT]
  J12 = Screw terminal - 2 pins [package=THT]
  J13 = Screw terminal - 2 pins [package=THT]
  J14 = Screw terminal - 2 pins [package=THT]
  J15 = Screw terminal - 2 pins [package=THT]
  J16 = Screw terminal - 2 pins [package=THT]
  J17 = Screw terminal - 2 pins [package=THT]
  J18 = Screw terminal - 2 pins [package=THT]
  J19 = Screw terminal - 2 pins [package=THT]
  J20 = Screw terminal - 2 pins [package=THT]
  J21 = Screw terminal - 2 pins [package=THT]
  J22 = Screw terminal - 2 pins [package=THT]
  J23 = Screw terminal - 2 pins [package=THT]
  J24 = Screw terminal - 2 pins [package=THT]
  J25 = Screw terminal - 2 pins [package=THT]
  J26 = Screw terminal - 2 pins [package=THT]
  S1 = Toggle Switch [package=THT]
  J27 = Screw terminal - 2 pins [package=THT]
  R36 = Resistor [tolerance=±5% resistance=10k package=THT]

nets:
  N1: Composant1.GND, R1.Pin_1, R2.Pin_1, R3.Pin_1, R4.Pin_1, R5.Pin_1, R6.Pin_1, R7.Pin_1, R8.Pin_1, R9.Pin_1, R10.Pin_1, R11.Pin_1, R12.Pin_1, R13.Pin_1, R14.Pin_1, R15.Pin_1, R16.Pin_1, R17.Pin_1, R21.Pin_1, R22.Pin_1, R23.Pin_1, R29.Pin_1, R30.Pin_1, R31.Pin_1, R32.Pin_1, R33.Pin_1, R35.Pin_1, R36.Pin_1
  N2: Composant1.5V, S1.COM, J27.pin1
  N3: Composant1.D2_PWM, S1.L2, J27.pin2, R36.Pin_0
  N4: Composant1.D22, LED3.anode, J1.pin2
  N5: Composant1.D23, LED4.anode, J2.pin2
  N6: Composant1.D24, LED6.anode, J3.pin2
  N7: Composant1.D25, LED7.anode, J4.pin2
  N8: Composant1.D26, LED8.anode, J8.pin2
  N9: Composant1.D27, LED11.anode, J6.pin2
  N10: Composant1.D28, LED9.anode, J5.pin2
  N11: Composant1.D29, LED10.anode, J7.pin2
  N12: Composant1.D30, LED15.anode, J15.pin2
  N13: Composant1.D31, LED16.anode, J12.pin2
  N14: Composant1.D32, LED14.anode, J9.pin2
  N15: Composant1.D33, LED19.anode, J16.pin2
  N16: Composant1.D34, LED17.anode, J13.pin2
  N17: Composant1.D35, LED13.anode, J10.pin2
  N18: Composant1.D36, LED18.anode, J14.pin2
  N19: Composant1.D37, LED12.anode, J11.pin2
  N20: Composant1.D38, LED23.anode, J23.pin2
  N21: Composant1.D39, LED24.anode, J20.pin2
  N22: Composant1.D40, LED22.anode, J17.pin2
  N23: Composant1.D41, LED27.anode, J24.pin2
  N24: Composant1.D42, LED38.anode, J22.pin2
  N25: Composant1.D43, LED29.anode, J19.pin2
  N26: Composant1.D44, LED28.anode, J21.pin2
  N27: Composant1.D45, LED34.anode, J18.pin2
  N28: Composant1.D46, LED42.anode, J25.pin2
  N29: Composant1.D47, LED41.anode, J26.pin2
  N30: LED3.cathode, R1.Pin_0, J1.pin1
  N31: LED4.cathode, R2.Pin_0, J2.pin1
  N32: LED6.cathode, R3.Pin_0, J3.pin1
  N33: LED7.cathode, R4.Pin_0, J4.pin1
  N34: LED8.cathode, R7.Pin_0, J8.pin1
  N35: LED9.cathode, R5.Pin_0, J5.pin1
  N36: LED10.cathode, R8.Pin_0, J7.pin1
  N37: LED11.cathode, R6.Pin_0, J6.pin1
  N38: LED12.cathode, R16.Pin_0, J11.pin1
  N39: LED13.cathode, R10.Pin_0, J10.pin1
  N40: LED14.cathode, R14.Pin_0, J9.pin1
  N41: LED15.cathode, R15.Pin_0, J15.pin1
  N42: LED16.cathode, R9.Pin_0, J12.pin1
  N43: LED17.cathode, R12.Pin_0, J13.pin1
  N44: LED18.cathode, R11.Pin_0, J14.pin1
  N45: LED19.cathode, R13.Pin_0, J16.pin1
  N46: LED22.cathode, R22.Pin_0, J17.pin1
  N47: LED23.cathode, R23.Pin_0, J23.pin1
  N48: LED24.cathode, R17.Pin_0, J20.pin1
  N49: LED27.cathode, R21.Pin_0, J24.pin1
  N50: LED28.cathode, R32.Pin_0, J21.pin1
  N51: LED29.cathode, R31.Pin_0, J19.pin1
  N52: LED34.cathode, R30.Pin_0, J18.pin1
  N53: LED38.cathode, R35.Pin_0, J22.pin1
  N54: LED41.cathode, R29.Pin_0, J26.pin1
  N55: LED42.cathode, R33.Pin_0, J25.pin1

notes:
  A  B
  C  D
  G  H
  E  F
  I  J
  K  L
  S  T
  Y  Z
  O  P
  Q  R
  W  X
  M  N
  U  V
