# Fritzing sketch id2879_ouija002_0 (saved by Fritzing 0.9.3b)
circuit board: 15.4948cm x 8.55059cm
breadboards: 2

parts:
  Composant1 = Arduino Mega 2560 (Rev3)
  R1 = Resistor [tolerance=±5% resistance=220 part_number=A package=THT]
  R2 = Resistor [tolerance=±5% resistance=220 part_number=B package=THT]
  R3 = Resistor [tolerance=±5% resistance=220 part_number=C package=THT]
  R4 = Resistor [tolerance=±5% resistance=220 part_number=D package=THT]
  R5 = Resistor [tolerance=±5% resistance=220 part_number=G package=THT]
  R6 = Resistor [tolerance=±5% resistance=220 part_number=F package=THT]
  R7 = Resistor [tolerance=±5% resistance=220 part_number=E package=THT]
  R8 = Resistor [tolerance=±5% resistance=220 part_number=H package=THT]
  R9 = Resistor [tolerance=±5% resistance=220 part_number=J package=THT]
  R10 = Resistor [tolerance=±5% resistance=220 part_number=N package=THT]
  R11 = Resistor [tolerance=±5% resistance=220 part_number=O package=THT]
  R12 = Resistor [tolerance=±5% resistance=220 part_number=M package=THT]
  R13 = Resistor [tolerance=±5% resistance=220 part_number=L package=THT]
  R14 = Resistor [tolerance=±5% resistance=220 part_number=K package=THT]
  R15 = Resistor [tolerance=±5% resistance=220 part_number=I package=THT]
  R16 = Resistor [tolerance=±5% resistance=220 part_number=P package=THT]
  R17 = Resistor [tolerance=±5% resistance=220 part_number=R package=THT]
  R21 = Resistor [tolerance=±5% resistance=220 part_number=T package=THT]
  R22 = Resistor [tolerance=±5% resistance=220 part_number=S package=THT]
  R23 = Resistor [tolerance=±5% resistance=220 part_number=Q package=THT]
  R29 = Resistor [tolerance=±5% resistance=220 part_number=Z package=THT]
  R30 = Resistor [tolerance=±5% resistance=220 part_number=X package=THT]
  R31 = Resistor [tolerance=±5% resistance=220 part_number=V package=THT]
  R32 = Resistor [tolerance=±5% resistance=220 part_number=W package=THT]
  R33 = Resistor [tolerance=±5% resistance=220 part_number=Y package=THT]
  R35 = Resistor [tolerance=±5% resistance=220 part_number=U package=THT]
  J1 = Screw terminal - 2 pins [part_number=A package=THT]
  J2 = Screw terminal - 2 pins [part_number=B package=THT]
  J3 = Screw terminal - 2 pins [part_number=C package=THT]
  J4 = Screw terminal - 2 pins [part_number=D package=THT]
  J5 = Screw terminal - 2 pins [part_number=G package=THT]
  J6 = Screw terminal - 2 pins [part_number=F package=THT]
  J7 = Screw terminal - 2 pins [part_number=H package=THT]
  J8 = Screw terminal - 2 pins [part_number=E package=THT]
  J9 = Screw terminal - 2 pins [part_number=K package=THT]
  J10 = Screw terminal - 2 pins [part_number=N package=THT]
  J11 = Screw terminal - 2 pins [part_number=P package=THT]
  J12 = Screw terminal - 2 pins [part_number=J package=THT]
  J13 = Screw terminal - 2 pins [part_number=M package=THT]
  J14 = Screw terminal - 2 pins [part_number=O package=THT]
  J15 = Screw terminal - 2 pins [part_number=I package=THT]
  J16 = Screw terminal - 2 pins [part_number=L package=THT]
  J17 = Screw terminal - 2 pins [part_number=S package=THT]
  J18 = Screw terminal - 2 pins [part_number=X package=THT]
  J19 = Screw terminal - 2 pins [part_number=V package=THT]
  J20 = Screw terminal - 2 pins [part_number=R package=THT]
  J21 = Screw terminal - 2 pins [part_number=W package=THT]
  J22 = Screw terminal - 2 pins [part_number=U package=THT]
  J23 = Screw terminal - 2 pins [part_number=Q package=THT]
  J24 = Screw terminal - 2 pins [part_number=T package=THT]
  J25 = Screw terminal - 2 pins [part_number=Y package=THT]
  J26 = Screw terminal - 2 pins [part_number=Z package=THT]
  J27 = Screw terminal - 2 pins [part_number=1 package=THT]
  R36 = Resistor [tolerance=±5% resistance=10k part_number=1 package=THT]

nets:
  N1: Composant1.5V, J27.pin1
  N2: Composant1.GND, R1.Pin_1, R2.Pin_1, R3.Pin_1, R4.Pin_1, R5.Pin_1, R6.Pin_1, R7.Pin_1, R8.Pin_1, R9.Pin_1, R10.Pin_1, R11.Pin_1, R12.Pin_1, R13.Pin_1, R14.Pin_1, R15.Pin_1, R16.Pin_1, R17.Pin_1, R21.Pin_1, R22.Pin_1, R23.Pin_1, R29.Pin_1, R30.Pin_1, R31.Pin_1, R32.Pin_1, R33.Pin_1, R35.Pin_1, R36.Pin_1
  N3: Composant1.D22, J1.pin2
  N4: Composant1.D23, J2.pin2
  N5: Composant1.D24, J3.pin2
  N6: Composant1.D25, J4.pin2
  N7: Composant1.D26, J8.pin2
  N8: Composant1.D27, J6.pin2
  N9: Composant1.D28, J5.pin2
  N10: Composant1.D29, J7.pin2
  N11: Composant1.D30, J15.pin2
  N12: Composant1.D31, J12.pin2
  N13: Composant1.D32, J9.pin2
  N14: Composant1.D33, J16.pin2
  N15: Composant1.D34, J13.pin2
  N16: Composant1.D35, J10.pin2
  N17: Composant1.D36, J14.pin2
  N18: Composant1.D37, J11.pin2
  N19: Composant1.D38, J23.pin2
  N20: Composant1.D39, J20.pin2
  N21: Composant1.D40, J17.pin2
  N22: Composant1.D41, J24.pin2
  N23: Composant1.D42, J22.pin2
  N24: Composant1.D43, J19.pin2
  N25: Composant1.D44, J21.pin2
  N26: Composant1.D45, J18.pin2
  N27: Composant1.D46, J25.pin2
  N28: Composant1.D47, J26.pin2
  N29: Composant1.D53, J27.pin2, R36.Pin_0
  N30: R1.Pin_0, J1.pin1
  N31: R2.Pin_0, J2.pin1
  N32: R3.Pin_0, J3.pin1
  N33: R4.Pin_0, J4.pin1
  N34: R5.Pin_0, J5.pin1
  N35: R6.Pin_0, J6.pin1
  N36: R7.Pin_0, J8.pin1
  N37: R8.Pin_0, J7.pin1
  N38: R9.Pin_0, J12.pin1
  N39: R10.Pin_0, J10.pin1
  N40: R11.Pin_0, J14.pin1
  N41: R12.Pin_0, J13.pin1
  N42: R13.Pin_0, J16.pin1
  N43: R14.Pin_0, J9.pin1
  N44: R15.Pin_0, J15.pin1
  N45: R16.Pin_0, J11.pin1
  N46: R17.Pin_0, J20.pin1
  N47: R21.Pin_0, J24.pin1
  N48: R22.Pin_0, J17.pin1
  N49: R23.Pin_0, J23.pin1
  N50: R29.Pin_0, J26.pin1
  N51: R30.Pin_0, J18.pin1
  N52: R31.Pin_0, J19.pin1
  N53: R32.Pin_0, J21.pin1
  N54: R33.Pin_0, J25.pin1
  N55: R35.Pin_0, J22.pin1

notes:
  connexions pour les LED de A à Z
  connexion pour le bouton
