# Fritzing sketch id287_Solucion_Esquema_Problema_1___Fritzing_0 (saved by Fritzing 0.9.3b)
breadboards: 1

parts:
  PANTALLA = LCD screen
  R1 = Trimmer Potentiometer [maximum_resistance=10kΩ package=THT]
  PLACA = Arduino Uno (Rev3)
  R2 = Resistor [tolerance=±5% resistance=220 package=THT]
  LED1 = LED - 5mm [color="Red (633nm)" package="5 mm [THT]"]
  J1 = Piezo Speaker
  RHT1 = Humidity and Temperature Sensor RHT03
  R4 = Resistor [tolerance=±5% resistance=100 package=THT]
  R5 = Resistor [tolerance=±5% resistance=330 package=THT]
  R6 = Resistor [tolerance=±5% resistance=330 package=THT]

nets:
  VSS: PANTALLA.VSS, PANTALLA.R/W, PANTALLA.LED-, R1.leg1, PLACA.GND, J1.pin1, RHT1.GND_2, R6.Pin_0
  VDD: PANTALLA.VDD, R1.leg2, PLACA.5V, R2.Pin_1, RHT1.Vcc, R5.Pin_0
  N1: PANTALLA.V0, R1.wiper
  N2: PANTALLA.RS, PLACA.D11_PWM/MOSI
  N3: PANTALLA.E, PLACA.D12/MISO
  N4: PANTALLA.DB4, PLACA.D5_PWM
  N5: PANTALLA.DB5, PLACA.D4
  N6: PANTALLA.DB6, PLACA.D3_PWM
  N7: PANTALLA.DB7, PLACA.D2
  N8: PANTALLA.LED+, R2.Pin_0
  N9: PLACA.D8, RHT1.Data-signal, R5.Pin_1
  N10: PLACA.D9_PWM, R4.Pin_1
  N11: PLACA.D7, LED1.anode
  N12: LED1.cathode, R6.Pin_1
  N13: J1.pin2, R4.Pin_0
