# Fritzing sketch id2880_ov_0 (saved by Fritzing 0.9.3b)
circuit board: 9.22174cm x 6.13352cm
breadboards: 1

parts:
  Onderdeel1 = adafruit [part_number="Adafruit #3405"]
  Onderdeel2 = SSOP28DB [chip_label=SSOP28DB package=SSOP]
  Onderdeel3 = adafruit [part_number=1393]
  ENCODER2 = Rotary_Encoder_with_Knob
  U2 = waveshare
  U6 = RJ45 Jack [package=rj45-8]
  U7 = RS232 Transceiver [package=so016]
  C1 = Capacitor [package=axial-5mm]
  C2 = Capacitor [package=axial-5mm]
  C3 = Capacitor [package=axial-5mm]
  C4 = Capacitor [package=axial-5mm]
  IC1 = Voltage Regulator [package=to220-igo]
  C5 = Capacitor [package=axial-5mm]
  C6 = Capacitor [package=axial-5mm]
  M1 = prefix0000
  C7 = Capacitor [package=axial-5mm]
  C9 = Capacitor [package=axial-5mm]

nets:
  N1: Onderdeel1.connector46, U7.R1OUT
  N2: Onderdeel1.connector47, U7.T1IN
  N3: Onderdeel1.connector49, U2.connector4
  N4: Onderdeel1.connector50, U2.connector5
  N5: Onderdeel1.connector52, ENCODER2.connector1
  N6: Onderdeel1.connector53, ENCODER2.connector2
  N7: Onderdeel1.connector54, ENCODER2.connector3
  N8: Onderdeel1.connector57, Onderdeel2.12, Onderdeel3.connector7, U2.connector2, U7.GND, C3.2, C4.2, C5.2
  N9: Onderdeel1.connector59, Onderdeel3.connector6, ENCODER2.connector5, U2.connector3, U7.VCC
  N10: Onderdeel1.connector63, Onderdeel2.1, Onderdeel2.15, IC1.OUT, C5.1, C6.2, C7.1
  N11: Onderdeel1.connector65, Onderdeel2.26
  N12: Onderdeel1.connector66, Onderdeel2.27
  N13: Onderdeel1.connector67, Onderdeel2.28
  N14: Onderdeel1.connector68, Onderdeel3.connector9
  N15: Onderdeel1.connector69, Onderdeel3.connector10
  N16: Onderdeel1.connector70, Onderdeel3.connector8
  N17: Onderdeel1.connector71, U2.connector8
  N18: Onderdeel1.connector72, U2.connector7
  N19: Onderdeel2.4, M1.connector2
  N20: Onderdeel2.5, M1.connector1
  N21: Onderdeel2.6, M1.connector4
  N22: Onderdeel2.7, M1.connector3
  N23: U6.1, U7.T1OUT
  N24: U6.2, U7.R1IN
  N25: U6.3, IC1.GND, C6.1, C7.2, C9.1
  N26: U6.4, IC1.IN, C9.2
  N27: U7.C1+, C1.1
  N28: U7.V+, C3.1
  N29: U7.C1-, C1.2
  N30: U7.C2+, C2.1
  N31: U7.C2-, C2.2
  N32: U7.V-, C4.1
