# Fritzing sketch id2881_ov7670_0 (saved by Fritzing 0.9.2b)
perfboards: 1
breadboards: 1

parts:
  Part1 = Arduino Uno (Rev3)
  R1 = Resistor [tolerance=±5% resistance=10k package=THT]
  R2 = Resistor [tolerance=±5% resistance=10k package=THT]

nets:
  N1: Part1.A4/SDA, R2.Pin_0
  N2: Part1.A5/SCL, R1.Pin_0
  N3: Part1.5V, R1.Pin_1, R2.Pin_1

notes:
  SIOD
  HREF
  GND
  XCLK
  D4
  D0
  D2
  VSYNC
  PCLK
  D1
  D7
  D3
  + VCC
  SIOC
  D5
  PWDN
  RESET
  OV7670
  D6
