# Fritzing sketch id2882_OvDuino_0 (saved by Fritzing 0.8.5b)
breadboards: 1

parts:
  LED1 = RGB LED (com. anode, rbg) [package="5 mm [THT]"]
  LED2 = RGB LED (com. anode, rbg) [package="5 mm [THT]"]
  LED3 = LED - 5mm [color="Red (633nm)" package="5 mm [THT]"]
  C1 = Electrolytic Capacitor [capacitance=0.1mF package="200 mil [THT, electrolytic]"]
  R1 = Resistor [tolerance=±5% resistance=220 package=THT]
  R2 = Resistor [tolerance=±5% resistance=220 package=THT]
  R3 = Resistor [tolerance=±5% resistance=220 package=THT]
  J1 = Basic Servo
  Componente1 = Arduino Uno (Rev3)
  IR1 = TSOP312.., 314.. [package=THT]

nets:
  N1: LED1.red_cathode, LED2.red_cathode, Componente1.D5_PWM
  GND: LED1.common_anode, LED2.common_anode, LED3.anode, C1.+, R1.Pin_1, R2.Pin_1, J1.gnd, Componente1.GND, IR1.GND
  N2: LED1.blue_cathode, LED2.blue_cathode, Componente1.D6_PWM
  N3: LED3.cathode, R3.Pin_1
  VCC: C1.-, J1.vcc, Componente1.5V, IR1.Vs
  N4: R3.Pin_0, Componente1.D7
  N5: Componente1.D11_PWM/MOSI, IR1.Data

notes:
  NUNCHUK - WII
  alimentazione 3,3 V]
