# Fritzing sketch id2885_Untitled_Sketch_4_0 (saved by Fritzing 0.9.2b)
breadboards: 1

parts:
  Parte1 = Arduino Uno (Rev3)
  LCD1 = LCD screen
  R1 = Rotary Potentiometer (Small) [maximum_resistance=100kΩ package=THT]

nets:
  N1: Parte1.D8, LCD1.RS
  N2: Parte1.D9_PWM, LCD1.DB4
  N3: Parte1.D10_PWM/SS, LCD1.DB5
  N4: Parte1.D11_PWM/MOSI, LCD1.DB6
  N5: Parte1.D12/MISO, LCD1.DB7
  N6: Parte1.D7, LCD1.VDD
  N7: Parte1.5V, LCD1.LED+, R1.leg2
  N8: Parte1.GND, LCD1.V0, LCD1.LED-, R1.leg1
  N9: LCD1.VSS, R1.wiper
