# Fritzing sketch id2887_PAOLO_Sketch_0 (saved by Fritzing 0.9.3b)
breadboards: 1

parts:
  Componente1 = Arduino Mega ADK (Rev3)
  R4 = Resistor [tolerance=±5% resistance=220 package=THT]
  R5 = Resistor [tolerance=±5% resistance=220 package=THT]
  LED1 = LED - 5mm [color="Green (570nm)" package="5 mm [THT]"]
  LED2 = LED - 5mm [color="Blue (430nm)" package="5 mm [THT]"]

nets:
  N1: Componente1.D13_PWM, LED2.cathode
  N2: Componente1.D11_PWM, LED1.cathode
  N3: Componente1.GND, R4.Pin_1, R5.Pin_1
  N4: R4.Pin_0, LED2.anode
  N5: R5.Pin_0, LED1.anode
