# Fritzing sketch id2888_ESQUEMA_PAP_0 (saved by Fritzing 0.9.3b)
breadboards: 1

parts:
  Arduino_Uno = Arduino Uno (Rev3)
  Módulo_de_ITEAD = Bluetooth HC-05 Macho
  J1 = Basic Servo
  Nivel_3 = LEDs [package=led10mm]
  Nivel_2 = LEDs [package=led10mm]
  Nivel_3_2 = LEDs [package=led10mm]
  ON = LEDs [package=led10mm]

nets:
  N1: Arduino_Uno.D9_PWM, J1.pulse
  N2: Arduino_Uno.D10_PWM/SS, Nivel_3.A
  N3: Arduino_Uno.D11_PWM/MOSI, Nivel_2.A
  N4: Arduino_Uno.D12/MISO, Nivel_3_2.A
  N5: Arduino_Uno.D13/SCK, ON.A
  GND: Arduino_Uno.GND, Módulo_de_ITEAD.GND, J1.gnd, Nivel_3.C, Nivel_2.C, Nivel_3_2.C, ON.C
  N6: Arduino_Uno.D4, Módulo_de_ITEAD.RXD
  N7: Arduino_Uno.D5_PWM, Módulo_de_ITEAD.TXD
  VCC: Arduino_Uno.5V, Módulo_de_ITEAD.VCC, J1.vcc
