# Fritzing sketch id2889_paper_plane_launcher_0 (saved by Fritzing 0.9.3b)
circuit board: 8.46667cm x 5.64444cm
breadboards: 1

parts:
  Q1 = NPN-Transistor [package="TO92 [THT]"]
  R1 = Resistor [tolerance=±5% resistance=220 package=THT]
  D1 = Rectifier Diode [part_number=1N4001 package="300 mil [THT]"]
  Part1 = Arduino-MKR1000
  M1 = DC Motor
  M2 = DC Motor

nets:
  N1: Q1.E, Part1.connector24
  N2: Q1.B, R1.Pin_1
  N3: Q1.C, D1.anode, M2.pin_2
  N4: R1.Pin_0, Part1.connector10
  N5: D1.cathode, Part1.connector25, M1.pin_1
  N6: M1.pin_2, M2.pin_1

notes:
  Bear in mind that I don't have much knowledge in electronics and that I'm not responsible for any damage to your parts.
