# Fritzing sketch id2890_arduino_shield_0 (saved by Fritzing 0.7.10b)
breadboards: 1

parts:
  Arduino1 = Arduino
  LED1 = LED - 5mm [color="Red (633nm)" package="5 mm [THT]"]
  LED2 = LED - 5mm [color="Red (633nm)" package="5 mm [THT]"]
  LED3 = LED - 5mm [color="Red (633nm)" package="5 mm [THT]"]
  LED4 = LED - 5mm [color="Red (633nm)" package="5 mm [THT]"]
  J1 = Screw terminal - 2 pins [package=THT]
  J2 = Screw terminal - 2 pins [package=THT]
  J3 = Screw terminal - 2 pins [package=THT]
  J4 = Screw terminal - 2 pins [package=THT]
  IC1 = H-Bridge [package=THT]
  M1 = DC Motor
  M2 = DC Motor

nets:
  GND: Arduino1.GND, LED1.anode, LED2.anode, LED3.anode, LED4.anode, IC1.GND1, IC1.GND2, IC1.GND3, IC1.GND4
  N1: Arduino1.D11, IC1.1A
  N2: Arduino1.D10, IC1.2A
  N3: Arduino1.D6, IC1.4A
  N4: Arduino1.D5, IC1.3A
  N5: Arduino1.D3, IC1.1_2EN
  N6: Arduino1.D2, IC1.3_4EN
  N7: Arduino1.3V3, J1.pin2, J2.pin2, J3.pin2, J4.pin2
  N8: Arduino1.+5V, IC1.VCC2, IC1.VCC1
  N9: Arduino1.A0, LED1.cathode, J2.pin1
  N10: Arduino1.A1, LED4.cathode, J1.pin1
  N11: Arduino1.A2, LED3.cathode, J3.pin1
  N12: Arduino1.A3, LED2.cathode, J4.pin1
  N13: IC1.1Y, M1.pin_1
  N14: IC1.2Y, M1.pin_2
  N15: IC1.3Y, M2.pin_2
  N16: IC1.4Y, M2.pin_1
