# Fritzing sketch id2892_parking_sensor_0 (saved by Fritzing 0.9.0b)
breadboards: 1

parts:
  Part1 = Arduino Uno (Rev3)
  J1 = Piezo Speaker [part_number=5V]
  R1 = Resistor [tolerance=±5% resistance=220 package=THT]
  LED1 = LED - 5mm [color="Red (633nm)" package="5 mm [THT]"]
  R2 = Resistor [tolerance=±5% resistance=220 package=THT]
  IC1 = 74HC595 [part_number="8 Bit Shift Register" package="DIP16 [THT]"]
  R3 = Resistor [tolerance=±5% resistance=220 package=THT]
  LED2 = LED - 5mm [color="Red (633nm)" package="5 mm [THT]"]
  R4 = Resistor [tolerance=±5% resistance=220 package=THT]
  LED3 = LED - 5mm [color="Red (633nm)" package="5 mm [THT]"]
  R5 = Resistor [tolerance=±5% resistance=220 package=THT]
  LED4 = LED - 5mm [color="Yellow (595nm)" package="5 mm [THT]"]
  R6 = Resistor [tolerance=±5% resistance=220 package=THT]
  LED5 = LED - 5mm [color="Yellow (595nm)" package="5 mm [THT]"]
  R7 = Resistor [tolerance=±5% resistance=220 package=THT]
  LED6 = LED - 5mm [color="Yellow (595nm)" package="5 mm [THT]"]
  R8 = Resistor [tolerance=±5% resistance=220 package=THT]
  LED7 = LED - 5mm [color="Green (565nm)" package="5 mm [THT]"]
  R9 = Resistor [tolerance=±5% resistance=220 package=THT]
  LED8 = LED - 5mm [color="Green (565nm)" package="5 mm [THT]"]

nets:
  N1: Part1.D11_PWM/MOSI, IC1.SH_CP
  N2: Part1.D12/MISO, IC1.ST_CP
  N3: Part1.D13/SCK, IC1.DS
  N4: Part1.D4, R1.Pin_1
  5V: Part1.5V, IC1.MR, IC1.VCC
  GND: Part1.GND, J1.pin1, R2.Pin_1, IC1.GND, IC1.OE, R3.Pin_1, R4.Pin_1, R5.Pin_1, R6.Pin_1, R7.Pin_1, R8.Pin_1, R9.Pin_1
  N5: J1.pin2, R1.Pin_0
  N6: LED1.cathode, R2.Pin_0
  N7: LED1.anode, IC1.Q7
  N8: IC1.Q1, LED7.anode
  N9: IC1.Q2, LED6.anode
  N10: IC1.Q3, LED5.anode
  N11: IC1.Q4, LED4.anode
  N12: IC1.Q5, LED3.anode
  N13: IC1.Q6, LED2.anode
  N14: IC1.Q0, LED8.anode
  N15: R3.Pin_0, LED2.cathode
  N16: R4.Pin_0, LED3.cathode
  N17: R5.Pin_0, LED4.cathode
  N18: R6.Pin_0, LED5.cathode
  N19: R7.Pin_0, LED6.cathode
  N20: R8.Pin_0, LED7.cathode
  N21: R9.Pin_0, LED8.cathode

notes:
  HC-SR04
  VCC TRIG ECHO GND
