# Fritzing sketch id2893_RPI_Gate_0 (saved by Fritzing 0.9.3b)
breadboards: 1

parts:
  Part1 = RFID - RC522
  Part2 = RFID - RC522
  Raspberry_Pi_1 = Raspberry Pi 3 [part_number=RPI-3-V1.2]
  D2F1 = D2F_FL_Omron_Snap_Action_Limit_Switch_with_Level
  D2F2 = D2F_FL_Omron_Snap_Action_Limit_Switch_with_Level
  D2F3 = D2F_FL_Omron_Snap_Action_Limit_Switch_with_Level
  D2F4 = D2F_FL_Omron_Snap_Action_Limit_Switch_with_Level
  J1 = Basic Servo
  J2 = Basic Servo

nets:
  N1: Part1.connector8, Raspberry_Pi_1.GPIO7
  N2: Part1.connector9, Part2.connector9, Raspberry_Pi_1.GPIO11
  N3: Part1.connector10, Part2.connector10, Raspberry_Pi_1.GPIO10
  N4: Part1.connector11, Part2.connector11, Raspberry_Pi_1.GPIO9
  GND: Part1.connector13, Part2.connector13, Raspberry_Pi_1.GND, J1.gnd, J2.gnd
  N5: Part1.connector14, Raspberry_Pi_1.GPIO23
  N6: Part1.connector15, Part2.connector15, Raspberry_Pi_1.3v3, D2F1.connector1, D2F2.connector1, D2F3.connector1, D2F4.connector1
  N7: Part2.connector8, Raspberry_Pi_1.GPIO8
  N8: Part2.connector14, Raspberry_Pi_1.GPIO24
  N9: Raspberry_Pi_1.GPIO5, D2F4.connector1pad_1
  N10: Raspberry_Pi_1.GPIO6, D2F3.connector1pad_1
  N11: Raspberry_Pi_1.GPIO13, D2F2.connector1pad_1
  N12: Raspberry_Pi_1.GPIO19, D2F1.connector1pad_1
  N13: Raspberry_Pi_1.GPIO20, J1.pulse
  N14: Raspberry_Pi_1.GPIO16, J2.pulse
  VCC: Raspberry_Pi_1.5V, J1.vcc, J2.vcc

notes:
  RFID Tags schematic:
  Don't follow the pin names
  clockwise from VCC:
  VCC = 3.3V
  IRQ = NC
  GND
  SDA
  SCK
  RST
  MOSI
  MISO
  Will develop a PCB when final schematics and specs are available.
