# Fritzing sketch id2894_Untitled_Sketch_0 (saved by Fritzing 0.7.10b)
breadboards: 1

parts:
  Arduino2 = Arduino
  LED1 = LED - 5mm [color="Red (633nm)" package="5 mm [THT]"]
  R1 = Resistor [tolerance=±5% resistance=510 package=THT]
  LED2 = LED - 5mm [color="Yellow (595nm)" package="5 mm [THT]"]
  R2 = Resistor [tolerance=±5% resistance=510 package=THT]

nets:
  N1: Arduino2.GND, LED1.cathode, LED2.cathode
  N2: Arduino2.D10, R2.Pin_1
  N3: Arduino2.D9, R1.Pin_0
  N4: LED1.anode, R2.Pin_0
  N5: R1.Pin_1, LED2.anode
