# Fritzing sketch id2895_PhotonBMP280_0 (saved by Fritzing 0.9.3b)
breadboards: 1

parts:
  Part1 = Photon
  Part2 = adafruit

nets:
  N1: Part1.GND, Part2.connector8
  N2: Part1.D0, Part2.connector11
  N3: Part1.D1, Part2.connector9
  N4: Part1.3V3, Part2.connector6
