# Fritzing sketch id2896_voltage_divider_0 (saved by Fritzing 0.9.2b)
breadboards: 1

parts:
  R1 = Resistor [tolerance=±5% resistance=220 package=THT]
  R2 = Resistor [tolerance=±5% resistance=680 package=THT]
  R3 = Resistor [tolerance=±5% resistance=330 package=THT]
  VCC1 = Battery block 9V
  Componente1 = Arduino Mega 2560 (Rev3)

nets:
  N1: R1.Pin_0, VCC1.+
  N2: R1.Pin_1, R2.Pin_0, Componente1.A0
  N3: R2.Pin_1, R3.Pin_0, Componente1.A1
  N4: R3.Pin_1, VCC1.-, Componente1.GND
