# Fritzing sketch id2897_obvod_pasak_pokus_0 (saved by Fritzing 0.9.3b)
circuit board: 5.9276cm x 3.84796cm
breadboards: 1

parts:
  IC1 = L293D [package=THT]
  BT1 = Bluetooth HC-06u
  U1 = atmega328 [package=dip]
  C1 = Ceramic Capacitor [capacitance=100nF package="100 mil [THT, multilayer]"]
  C2 = Ceramic Capacitor [capacitance=100nF package="100 mil [THT, multilayer]"]
  C3 = Electrolytic Capacitor [capacitance=22µF package="100 mil [THT, electrolytic]"]
  U2 = Voltage Regulator - 5V [package="TO220 [THT]"]
  R1 = Resistor [tolerance=±5% resistance=10k package=THT]
  C4 = Ceramic Capacitor [capacitance=100nF package="100 mil [THT, multilayer]"]
  C5 = Ceramic Capacitor [capacitance=100nF package="100 mil [THT, multilayer]"]
  XTAL1 = Crystal [frequency="16 Mhz" package=THT]
  C6 = Ceramic Capacitor [capacitance=100nF package="100 mil [THT, multilayer]"]
  hc-sr1 = hc-sr04
  C7 = Ceramic Capacitor [capacitance=100nF package="100 mil [THT, multilayer]"]
  C8 = Ceramic Capacitor [capacitance=100nF package="100 mil [THT, multilayer]"]
  C9 = Ceramic Capacitor [capacitance=100nF package="100 mil [THT, multilayer]"]
  C10 = Ceramic Capacitor [capacitance=100nF package="100 mil [THT, multilayer]"]
  C11 = Electrolytic Capacitor [capacitance=0.47mF voltage=16V package="100 mil [THT, electrolytic]"]
  C12 = Ceramic Capacitor [capacitance=100nF package="100 mil [THT, multilayer]"]
  U3 = atmega328 [package=dip]
  R2 = Resistor [tolerance=±5% resistance=10k package=THT]
  C13 = Ceramic Capacitor [capacitance=100nF package="100 mil [THT, multilayer]"]
  C14 = Ceramic Capacitor [capacitance=100nF package="100 mil [THT, multilayer]"]
  XTAL2 = Crystal [frequency="16 Mhz" package=THT]
  J1 = female pin header, 4 pins [form="♀ (female)"]
  J2 = male pin header, 2 pins [form="♂ (male)"]
  J3 = male pin header, 3 pins [form="♂ (male)"]
  J4 = male pin header, 3 pins [form="♂ (male)"]

nets:
  N1: IC1.Enable_1, U1.D6_(PWM)
  N2: IC1.In_1, U1.D8
  N3: IC1.Out_1_(_Controlled_by_Enable_1_), C9.0, J1.pin3
  GND: IC1.0V, BT1.connector1, U1.GND#7, C1.1, C2.1, C3.-, U2.GND, C4.1, C5.1, C6.1, hc-sr1.GND, C7.1, C8.0, C9.1, C10.0, C11.-, C12.1, U3.GND#7, C13.1, C14.1, J2.pin1, J3.pin3, J4.pin3
  N4: IC1.Out_2_(_Controlled_by_Enable_1_), C10.1, J1.pin4
  N5: IC1.In_2, U1.D9_(PWM)
  N6: IC1.+Vmotor, U2.input_voltage, J2.pin2, J3.pin2, J4.pin2
  N7: IC1.Enable_2, U1.D5_(PWM)
  N8: IC1.In_3, U1.D7
  N9: IC1.Out_3_(_Controlled_by_Enable_2_), C8.1, J1.pin1
  N10: IC1.Out_4_(_Controlled_by_Enable_2_), C7.0, J1.pin2
  N11: IC1.In_4, U1.D4
  VCC: IC1.+V, BT1.connector0, U1.VCC, C1.0, C2.0, C3.+, U2.output_voltage, R1.Pin_0, C6.0, hc-sr1.VCC, C11.+, C12.0, U3.VCC, R2.Pin_0
  N12: BT1.connector2, U1.D2
  N13: BT1.connector3, U1.D3_(PWM)
  N14: U1.RESET, R1.Pin_1
  N15: U1.XLAT1, C4.0, XTAL1.pin_0
  N16: U1.XLAT2, C5.0, XTAL1.pin_1
  N17: U1.D10_(PWM), hc-sr1.Echo
  N18: U1.D11_(PWM), hc-sr1.Trig
  N19: U1.A4, U3.A4
  N20: U1.A5, U3.A5
  N21: U3.RESET, R2.Pin_1
  N22: U3.XLAT1, C13.0, XTAL2.pin_0
  N23: U3.XLAT2, C14.0, XTAL2.pin_1
  N24: U3.D9_(PWM), J3.pin1
  N25: U3.D10_(PWM), J4.pin1
