# Fritzing sketch id2898_Password_0 (saved by Fritzing 0.8.3b)
breadboards: 1

parts:
  Part1 = Arduino Uno (Rev3)
  U1 = LCD-16X2 [package=lcd-16x2]
  R1 = Rotary Potentiometer (Small)
  R2 = Resistor [tolerance=±5% resistance=22k package="0603 [SMD]"]
  J1 = Basic Servo
  R3 = Photocell (LDR) [package=THT]
  LED1 = smd LED [color="Red (633nm)" package="0805 [SMD]"]
  LED2 = smd LED [color="Green (555nm)" package="0805 [SMD]"]
  S1 = Momentary Switch [package=ksa_sealed_tac_switch]
  KEYPAD1 = Membrane_Matrix_Keypad
  J2 = Piezo Speaker

nets:
  N1: Part1.A0, KEYPAD1.connector7
  N2: Part1.A1, KEYPAD1.connector6
  N3: Part1.A2, KEYPAD1.connector5
  N4: Part1.A3, KEYPAD1.connector4
  N5: Part1.A4/SDA, KEYPAD1.connector3
  N6: Part1.ICSP_SCK, Part1.D13/SCK, R2.Pin_0
  N7: Part1.D8, U1.DB4
  N8: Part1.D9_PWM, J1.pulse
  N9: Part1.D10_PWM/SS, U1.DB5
  N10: Part1.D11_PWM/MOSI, U1.DB6
  N11: Part1.D12/MISO, U1.DB7
  N12: Part1.D2, LED2.anode
  N13: Part1.D3_PWM, LED1.anode
  N14: Part1.D4, KEYPAD1.connector2
  N15: Part1.D5_PWM, KEYPAD1.connector1
  N16: Part1.D6_PWM, U1.RS
  N17: Part1.D7, U1.E
  N18: Part1.RESET, S1.1, S1.3
  VSS: U1.VSS, U1.R_W, U1.K, R1.leg2, J1.gnd, LED1.cathode, LED2.cathode, J2.pin1
  VDD: U1.VDD, U1.A, R1.leg1, J1.vcc, R3.pin_1
  N19: U1.VO, R1.wiper
  N20: R2.Pin_1, S1.2, S1.4, J2.pin2
