# Fritzing sketch id28_layout100ohm_0 (saved by Fritzing 0.9.2b)
circuit board: 3.5cm x 4.7cm
breadboards: 1

parts:
  JP1 = Header 12 [package=1x12_machine-pin-header_lock.004]
  JP2 = Header 12 [package=1x12_machine-pin-header_lock.004]
  R1 = Resistor [tolerance=±5% resistance=100 package=THT]
  R2 = Resistor [tolerance=±5% resistance=100 package=THT]
  R3 = Resistor [tolerance=±5% resistance=100 package=THT]
  R4 = Resistor [tolerance=±5% resistance=100 package=THT]
  R5 = Resistor [tolerance=±5% resistance=100 package=THT]
  R6 = Resistor [tolerance=±5% resistance=100 package=THT]
  R7 = Resistor [tolerance=±5% resistance=100 package=THT]
  R8 = Resistor [tolerance=±5% resistance=100 package=THT]
  R9 = Resistor [tolerance=±5% resistance=100 package=THT]
  R10 = Resistor [tolerance=±5% resistance=100 package=THT]
  R11 = Resistor [tolerance=±5% resistance=100 package=THT]
  R12 = Resistor [tolerance=±5% resistance=100 package=THT]
  JP3 = Header 12 [package=1x12_machine-pin-header_lock.004]
  U1 = mystery part, 12 pins [chip_label=?]
  JP4 = Header 12 [package=1x12_machine-pin-header_lock.004]
  U2 = mystery part, 12 pins [chip_label=?]

nets:
  N1: JP1.1, R1.Pin_1
  N2: JP1.2, R2.Pin_1
  N3: JP1.3, R3.Pin_1
  N4: JP1.4, R4.Pin_1
  N5: JP1.5, R5.Pin_1
  N6: JP1.6, R6.Pin_1
  N7: JP1.7, R7.Pin_1
  N8: JP1.8, R8.Pin_1
  N9: JP1.9, R9.Pin_1
  N10: JP1.10, R10.Pin_1
  N11: JP1.11, R11.Pin_1
  N12: JP1.12, R12.Pin_1
  N13: JP2.1, R1.Pin_0
  N14: JP2.2, R2.Pin_0
  N15: JP2.3, R3.Pin_0
  N16: JP2.4, R4.Pin_0
  N17: JP2.5, R5.Pin_0
  N18: JP2.6, R6.Pin_0
  N19: JP2.7, R7.Pin_0
  N20: JP2.8, R8.Pin_0
  N21: JP2.9, R9.Pin_0
  N22: JP2.10, R10.Pin_0
  N23: JP2.11, R11.Pin_0
  N24: JP2.12, R12.Pin_0
  N25: JP3.1, U1.pin1
  N26: JP3.2, U1.pin2
  N27: JP3.3, U1.pin3
  N28: JP3.4, U1.pin4
  N29: JP3.5, U1.pin5
  N30: JP3.6, U1.pin6
  N31: JP3.7, U1.pin7
  N32: JP3.8, U1.pin8
  N33: JP3.9, U1.pin9
  N34: JP3.10, U1.pin10
  N35: JP3.11, U1.pin11
  N36: JP3.12, U1.pin12
  N37: JP4.1, U2.pin1
  N38: JP4.2, U2.pin2
  N39: JP4.3, U2.pin3
  N40: JP4.4, U2.pin4
  N41: JP4.5, U2.pin5
  N42: JP4.6, U2.pin6
  N43: JP4.7, U2.pin7
  N44: JP4.8, U2.pin8
  N45: JP4.9, U2.pin9
  N46: JP4.10, U2.pin10
  N47: JP4.11, U2.pin11
  N48: JP4.12, U2.pin12
