# Fritzing sketch id2900_DAQ_0 (saved by Fritzing 0.9.0b)
circuit board: 8.15305cm x 5.74935cm
breadboards: 1

parts:
  DB25F = DB25F
  R1 = Resistor [tolerance=±5% resistance=100 package=THT]
  R2 = Resistor [tolerance=±5% resistance=100 package=THT]
  U1 = IC, DIP package, 4 pins [chip_label=IC]
  U2 = IC, DIP package, 4 pins [chip_label=IC]
  CON1 = screw terminal, 4 pins
  RELAY1 = Componente_sem_nome
  RELAY2 = Componente_sem_nome
  JACK_CON = Power plug
  R3 = Resistor [tolerance=±5% resistance=220 package=THT]
  LED1 = LED - 5mm [color="Red (633nm)" package="5 mm [THT]"]
  LED2 = LED - 5mm [color="Red (633nm)" package="5 mm [THT]"]
  LED3 = LED - 5mm [color="Red (633nm)" package="5 mm [THT]"]
  R4 = Resistor [tolerance=±5% resistance=220 package=THT]
  R5 = Resistor [tolerance=±5% resistance=220 package=THT]
  ULN2803 = IC, DIP package, 18 pins [chip_label=IC]

nets:
  N1: DB25F.pin1, R2.Pin_0
  N2: DB25F.pin2, R1.Pin_0
  N3: DB25F.pin15, U1.pin2, U2.pin2
  N4: R1.Pin_1, U1.pin1
  N5: R2.Pin_1, U2.pin1
  N6: U1.pin3, ULN2803.pin1
  N7: U1.pin4, U2.pin4, RELAY1.connector1, RELAY2.connector1, JACK_CON.VCC, LED1.anode, ULN2803.pin10
  N8: U2.pin3, ULN2803.pin2
  N9: CON1.pin1, RELAY2.connector3
  N10: CON1.pin2, RELAY2.connector2
  N11: CON1.pin3, RELAY1.connector3
  N12: CON1.pin4, RELAY1.connector2
  N13: RELAY1.connector0, LED3.anode, ULN2803.pin17
  N14: RELAY2.connector0, LED2.anode, ULN2803.pin18
  N15: JACK_CON.GND, R3.Pin_1, R4.Pin_1, R5.Pin_1, ULN2803.pin9
  N16: R3.Pin_0, LED1.cathode
  N17: LED2.cathode, R4.Pin_0
  N18: LED3.cathode, R5.Pin_0

notes:
  www.7t3visions.com
  100
  220k
