# Fritzing sketch id2901_webiopi_typeB_mini_0 (saved by Fritzing 0.9.2b)
circuit board: 2.5cm x 2.5cm
breadboards: 1

parts:
  Q1 = NPN-Transistor [part_number=2N3904T package="TO92 [THT]"]
  R1 = Resistor [tolerance=±5% resistance=10k package=THT]
  R2 = Resistor [tolerance=±5% resistance=10k package=THT]
  R3 = Resistor [tolerance=±5% resistance=10k package=THT]
  Q2 = NPN-Transistor [part_number=2N3904T package="TO92 [THT]"]
  R4 = Resistor [tolerance=±5% resistance=10k package=THT]
  R5 = Resistor [tolerance=±5% resistance=10k package=THT]
  IN = double row male pin header, 2 pins [form="♂ (male)"]
  C2 = Ceramic Capacitor [capacitance=10nF package="100 mil [THT, multilayer]"]
  Q3 = NPN-Transistor [part_number=2N3904T package="TO92 [THT]"]
  C1 = Ceramic Capacitor [capacitance=10nF package="100 mil [THT, multilayer]"]
  R7 = Resistor [tolerance=±5% resistance=10k package=THT]
  OUT = double row male pin header, 2 pins [form="♂ (male)"]
  R6 = Resistor [tolerance=±5% resistance=10k package=THT]
  J1 = double row female pin header, 12 pins [form="♀ (female)"]
  R8 = Resistor [tolerance=±5% resistance=10k package=THT]

nets:
  GND: Q1.E, R2.Pin_1, Q2.E, R4.Pin_1, IN.pin1, C2.0, Q3.E, C1.0, R7.Pin_1, OUT.pin2, J1.pin3, J1.pin8
  N1: Q1.B, R1.Pin_1, R2.Pin_0
  N2: Q1.C, R3.Pin_1, Q2.B, R4.Pin_0
  N3: R1.Pin_0, IN.pin2, C2.1
  N4: R3.Pin_0, R5.Pin_0, C1.1, J1.pin12
  N5: Q2.C, R5.Pin_1, J1.pin9
  N6: Q3.B, R7.Pin_0, R6.Pin_1
  N7: Q3.C, OUT.pin1, R8.Pin_1
  N8: R6.Pin_0, J1.pin6
  N9: J1.pin1, J1.pin2, R8.Pin_0

notes:
  TNPS001
