# Fritzing sketch id2902_RaspiForest_PCB_v7_0 (saved by Fritzing 0.9.2b)
circuit board: 8.38364cm x 17.0367cm

parts:
  J3 = male pin header, 10 pins [form="♂ (male)"]
  J4 = male pin header, 8 pins [form="♂ (male)"]
  J5 = male pin header, 8 pins [form="♂ (male)"]
  J6 = male pin header, 6 pins [form="♂ (male)"]
  GPIO_-_RPI_HIJITO = double row female pin header, 40 pins [form="♀ (female)"]
  Switch_Papa = Ceramic Capacitor [capacitance=100nF package="100 mil [THT, multilayer]"]
  Switch_Hijito = Ceramic Capacitor [capacitance=100nF package="100 mil [THT, multilayer]"]
  GPIO_-_RPI_PAPA = double row female pin header, 40 pins [form="♀ (female)"]
  VCC1 = Battery
  Transistor_NPN_(3204) = NPN-Transistor [package="TO92 [THT]"]
  Diodo = Rectifier Diode [part_number=1N4001 package="300 mil [THT]"]
  Relevo = RELAY-2 [package=relay-g5v]
  RTC_(DS-1307) = Real Time Clock Module - DS1307 RTC Breakout Board
  Digital_Level_Converter = Logic Level Converter

nets:
  N1: J3.pin4, GPIO_-_RPI_PAPA.pin23, GPIO_-_RPI_PAPA.pin27, VCC1.-, Transistor_NPN_(3204).E, Digital_Level_Converter.GND
  N2: J4.pin6, Transistor_NPN_(3204).B
  N3: J4.pin7, Digital_Level_Converter.RX2_HV
  N4: J4.pin8, Digital_Level_Converter.TX2_HV
  N5: J5.pin5, GPIO_-_RPI_HIJITO.pin22, GPIO_-_RPI_PAPA.pin21, VCC1.+, Diodo.cathode, Relevo.6, RTC_(DS-1307).5V, Digital_Level_Converter.HV
  N6: J5.pin6, RTC_(DS-1307).GND
  N7: J6.pin5, RTC_(DS-1307).SDA
  N8: J6.pin6, RTC_(DS-1307).SCL
  N9: GPIO_-_RPI_HIJITO.pin23, GPIO_-_RPI_PAPA.pin16
  N10: Switch_Papa.0, Switch_Hijito.0, Relevo.2
  N11: Switch_Papa.1, Switch_Hijito.1, Relevo.1
  N12: GPIO_-_RPI_PAPA.pin20, Digital_Level_Converter.LV
  N13: GPIO_-_RPI_PAPA.pin24, Digital_Level_Converter.TX2_LV
  N14: GPIO_-_RPI_PAPA.pin25, Digital_Level_Converter.RX2_LV
  N15: Transistor_NPN_(3204).C, Diodo.anode, Relevo.5

notes:
  El cable gris y blanco que salen del relevo se conectan a los pines de reset de las raspbberries pi A (Estos pines no aparecen en los diagramas esquemáticos de Fritzing)
  El relay que se usó en el proyecto raspi Forest es diferente. El número serial es SRC 06VDC - SH. Las salidas a las raspberries deben ser los conectores que normalmente están abiertos.
  El sistema se alimenta con 5V. Entonces, acá debería ponerse un adaptador de 12V a 5V (mas o menos 800 mA). La fuente de energía es una bareria de carro a 12V.s
  Raspberry papá: Tiene conectada la cámara RGB (verde)
  Raspberry hijito: Tiene conectada la cámara NOIR (negra)
  Maria Paula - Raspiforest
