# Fritzing sketch id2903_impreso_0 (saved by Fritzing 0.7.10b)
breadboards: 1

parts:
  R3 = Resistor [tolerance=±5% resistance=220 package=THT]
  R2 = Resistor [tolerance=±5% resistance=220 package=THT]
  R1 = Resistor [tolerance=±5% resistance=220 package=THT]
  R4 = Resistor [tolerance=±5% resistance=220 package=THT]
  R5 = Resistor [tolerance=±5% resistance=220 package=THT]
  R6 = Basic Flex Resistor
  R7 = Basic Flex Resistor
  R8 = Basic Flex Resistor
  J2 = Basic Servo
  J3 = Basic Servo
  J4 = Basic Servo
  J7 = female pin header, 2 pins [form="♀ (female)"]
  S3 = Pushbutton [package=THT]
  S4 = Pushbutton [package=THT]
  J1 = female pin header, 3 pins [form="♀ (female)"]
  Arduino1 = Arduino
  VCC1 = Battery
  J8 = Basic Servo
  J6 = male pin header, 4 pins [form="♂ (male)"]

nets:
  N1: R3.Pin_0, R2.Pin_0, R1.Pin_0, R4.Pin_1, R5.Pin_1, Arduino1.+5V
  N2: R3.Pin_1, R8.pin_1, Arduino1.A0
  N3: R2.Pin_1, R7.pin_1, Arduino1.A1
  N4: R1.Pin_1, R6.pin_1, Arduino1.A2
  N5: R4.Pin_0, S3.leg1, Arduino1.D2
  N6: R5.Pin_0, S4.leg1, Arduino1.D3
  GND: R6.Pin_2, R7.Pin_2, R8.Pin_2, J2.gnd, J3.gnd, J4.gnd, J7.pin1, J7.pin2, S3.leg0, S4.leg0, J1.pin1, J1.pin2, J1.pin3, Arduino1.GND, VCC1.-, J8.gnd, J6.pin1, J6.pin2, J6.pin3, J6.pin4
  VCC: J2.vcc, J3.vcc, J4.vcc, Arduino1.VIN, VCC1.+, J8.vcc
  N7: J2.pulse, Arduino1.D7
  N8: J3.pulse, Arduino1.D10
  N9: J4.pulse, Arduino1.D11
  N10: Arduino1.D6, J8.pulse
