# Fritzing sketch id2904_4x4x4_Matrix_2_routed2_0 (saved by Fritzing 0.8.7b)
circuit board: 10cm x 10cm
breadboards: 1

parts:
  J1 = female pin header, 1 pin [form="♀ (female)"]
  J2 = female pin header, 1 pin [form="♀ (female)"]
  J3 = female pin header, 1 pin [form="♀ (female)"]
  J4 = female pin header, 1 pin [form="♀ (female)"]
  J5 = female pin header, 1 pin [form="♀ (female)"]
  J6 = female pin header, 1 pin [form="♀ (female)"]
  J7 = female pin header, 1 pin [form="♀ (female)"]
  J8 = female pin header, 1 pin [form="♀ (female)"]
  J9 = female pin header, 1 pin [form="♀ (female)"]
  J10 = female pin header, 1 pin [form="♀ (female)"]
  J11 = female pin header, 1 pin [form="♀ (female)"]
  J12 = female pin header, 1 pin [form="♀ (female)"]
  J13 = female pin header, 1 pin [form="♀ (female)"]
  J14 = female pin header, 1 pin [form="♀ (female)"]
  J15 = female pin header, 1 pin [form="♀ (female)"]
  J16 = female pin header, 1 pin [form="♀ (female)"]
  J17 = female pin header, 1 pin [form="♀ (female)"]
  J18 = female pin header, 1 pin [form="♀ (female)"]
  J19 = female pin header, 1 pin [form="♀ (female)"]
  J20 = female pin header, 1 pin [form="♀ (female)"]
  J21 = female pin header, 1 pin [form="♀ (female)"]
  J22 = female pin header, 1 pin [form="♀ (female)"]
  J23 = female pin header, 1 pin [form="♀ (female)"]
  J24 = female pin header, 1 pin [form="♀ (female)"]
  J25 = female pin header, 1 pin [form="♀ (female)"]
  J26 = female pin header, 1 pin [form="♀ (female)"]
  J27 = female pin header, 1 pin [form="♀ (female)"]
  J28 = female pin header, 1 pin [form="♀ (female)"]
  J29 = female pin header, 1 pin [form="♀ (female)"]
  J30 = female pin header, 1 pin [form="♀ (female)"]
  J31 = female pin header, 1 pin [form="♀ (female)"]
  J32 = female pin header, 1 pin [form="♀ (female)"]
  J33 = female pin header, 1 pin [form="♀ (female)"]
  J34 = female pin header, 1 pin [form="♀ (female)"]
  J35 = female pin header, 1 pin [form="♀ (female)"]
  J37 = female pin header, 1 pin [form="♀ (female)"]
  J38 = female pin header, 1 pin [form="♀ (female)"]
  J39 = female pin header, 1 pin [form="♀ (female)"]
  J40 = female pin header, 1 pin [form="♀ (female)"]
  J41 = female pin header, 1 pin [form="♀ (female)"]
  J42 = female pin header, 1 pin [form="♀ (female)"]
  J44 = female pin header, 1 pin [form="♀ (female)"]
  J45 = female pin header, 1 pin [form="♀ (female)"]
  J46 = female pin header, 1 pin [form="♀ (female)"]
  J47 = female pin header, 1 pin [form="♀ (female)"]
  J48 = female pin header, 1 pin [form="♀ (female)"]
  J49 = female pin header, 1 pin [form="♀ (female)"]
  J50 = female pin header, 1 pin [form="♀ (female)"]
  J51 = female pin header, 1 pin [form="♀ (female)"]
  J52 = female pin header, 1 pin [form="♀ (female)"]
  J53 = female pin header, 1 pin [form="♀ (female)"]
  J54 = female pin header, 1 pin [form="♀ (female)"]
  J55 = female pin header, 1 pin [form="♀ (female)"]
  J56 = female pin header, 1 pin [form="♀ (female)"]
  J57 = female pin header, 1 pin [form="♀ (female)"]
  J58 = female pin header, 1 pin [form="♀ (female)"]
  J59 = female pin header, 1 pin [form="♀ (female)"]
  J60 = female pin header, 1 pin [form="♀ (female)"]
  J61 = female pin header, 1 pin [form="♀ (female)"]
  J62 = female pin header, 1 pin [form="♀ (female)"]
  J63 = female pin header, 1 pin [form="♀ (female)"]
  J64 = female pin header, 1 pin [form="♀ (female)"]
  J65 = single row smd female pin header, 13 pins [form="♀ (female)"]
  J66 = single row smd female pin header, 13 pins [form="♀ (female)"]
  J36 = female pin header, 1 pin [form="♀ (female)"]
  J43 = female pin header, 1 pin [form="♀ (female)"]
  Pad3 = Pad [width=2.54 height=2.54 connect=center]  # not connected
  Pad4 = Pad [width=2.54 height=2.54 connect=center]  # not connected
  Pad2 = Pad [width=2.54 height=2.54 connect=center]  # not connected
  Pad1 = Pad [width=2.54 height=2.54 connect=center]  # not connected

nets:
  N1: J1.pin1, J5.pin1, J11.pin1, J13.pin1, J65.pin6
  N2: J2.pin1, J17.pin1, J51.pin1, J52.pin1, J65.pin10
  N3: J3.pin1, J28.pin1, J50.pin1, J53.pin1, J66.pin1
  N4: J4.pin1, J21.pin1, J35.pin1, J39.pin1, J66.pin7
  N5: J6.pin1, J20.pin1, J33.pin1, J38.pin1, J65.pin9
  N6: J7.pin1, J19.pin1, J42.pin1, J65.pin13, J36.pin1
  N7: J8.pin1, J27.pin1, J34.pin1, J66.pin4, J43.pin1
  N8: J9.pin1, J23.pin1, J46.pin1, J57.pin1, J65.pin12
  N9: J10.pin1, J18.pin1, J54.pin1, J59.pin1, J65.pin8
  N10: J12.pin1, J26.pin1, J47.pin1, J58.pin1, J66.pin5
  N11: J14.pin1, J30.pin1, J41.pin1, J49.pin1, J65.pin11
  N12: J15.pin1, J22.pin1, J48.pin1, J55.pin1, J65.pin7
  N13: J16.pin1, J29.pin1, J44.pin1, J56.pin1, J66.pin6
  N14: J24.pin1, J25.pin1, J31.pin1, J32.pin1, J65.pin5
  N15: J37.pin1, J45.pin1, J63.pin1, J64.pin1, J65.pin3
  N16: J40.pin1, J60.pin1, J61.pin1, J62.pin1, J65.pin4

notes:
  Front
  4×4x4 RGB Charliecube
  http://aglick.com/charliecube.html
  PCB by Kjetilei
  Arduino Nano V3.0
  D2
  D12
  D13
  A0
  A3
