# Fritzing sketch id2907_CIMPRESO_0 (saved by Fritzing 0.7.1b)
breadboards: 1

parts:
  IC1 = L293D [package=THT]
  J2 = female pin header, 2 pins [form="♀ (female)"]
  J3 = female pin header, 2 pins [form="♀ (female)"]
  D1 = Rectifier Diode [part_number=1N4001 package="300 mil [THT]"]
  D2 = Rectifier Diode [part_number=1N4001 package="300 mil [THT]"]
  D3 = Rectifier Diode [part_number=1N4001 package="300 mil [THT]"]
  D4 = Rectifier Diode [part_number=1N4001 package="300 mil [THT]"]
  D5 = Rectifier Diode [part_number=1N4001 package="300 mil [THT]"]
  D6 = Rectifier Diode [part_number=1N4001 package="300 mil [THT]"]
  D7 = Rectifier Diode [part_number=1N4001 package="300 mil [THT]"]
  D8 = Rectifier Diode [part_number=1N4001 package="300 mil [THT]"]
  J5 = Screw terminal - 2 pins [package=THT]
  J6 = Screw terminal - 2 pins [package=THT]
  Arduino1 = Arduino
  J7 = female pin header, 2 pins [form="♀ (female)"]
  J8 = female pin header, 2 pins [form="♀ (female)"]

nets:
  N1: IC1.Enable_1, Arduino1.D3
  N2: IC1.In_1, Arduino1.D4
  N3: IC1.Out_1_(_Controlled_by_Enable_1_), D5.anode, D6.cathode, J5.pin2
  N4: IC1.0V, D2.anode, D6.anode, Arduino1.GND, J7.pin1, J7.pin2, J8.pin1, J8.pin2
  N5: IC1.Out_2_(_Controlled_by_Enable_1_), D1.anode, D2.cathode, J5.pin1
  N6: IC1.In_2, Arduino1.D9
  N7: IC1.+Vmotor, D1.cathode, D5.cathode
  N8: IC1.Enable_2, Arduino1.D11
  N9: IC1.In_3, Arduino1.D10
  N10: IC1.Out_3_(_Controlled_by_Enable_2_), D3.anode, D7.cathode, J6.pin1
  N11: IC1.Out_4_(_Controlled_by_Enable_2_), D4.anode, D8.cathode, J6.pin2
  N12: IC1.In_4, Arduino1.D2
  N13: IC1.+V, J2.pin1, J2.pin2, J3.pin1, J3.pin2, Arduino1.+5V
  N14: D3.cathode, D4.cathode
  N15: D7.anode, D8.anode
