# Fritzing sketch id2908_circuit_0 (saved by Fritzing 0.9.3b)
circuit board: 5cm x 5cm
breadboards: 1

parts:
  R1 = Resistor [tolerance=±5% resistance=470k package=THT]
  C1 = Ceramic Capacitor [capacitance=0.47µF voltage=12V package="100 mil [THT, multilayer]"]
  Power_plug1 = Power plug
  D1 = Rectifier Diode [part_number=1N4007 package="300 mil [THT]"]
  D2 = Rectifier Diode [part_number=1N4007 package="300 mil [THT]"]
  D3 = Rectifier Diode [part_number=1N4001 package="300 mil [THT]"]
  D4 = Rectifier Diode [part_number=1N4001 package="300 mil [THT]"]
  R5 = Resistor [tolerance=±5% resistance=220 package=THT]
  C2 = Ceramic Capacitor [capacitance=1mF package="100 mil [THT, multilayer]"]
  D5 = Zener Diode [part_number=1N4732A breakdown_voltage=5.1V package="Melf DO-213 AB [SMD]"]
  R4 = Resistor [tolerance=±5% resistance=100 package=THT]

nets:
  N1: R1.Pin_0, C1.1, Power_plug1.GND
  N2: R1.Pin_1, C1.0, D1.cathode, D2.anode
  N3: Power_plug1.VCC, R4.Pin_0
  N4: D1.anode, D3.anode, C2.0, D5.anode
  N5: D2.cathode, D4.cathode, R5.Pin_0, C2.1
  N6: D3.cathode, D4.anode, R4.Pin_1
  N7: R5.Pin_1, D5.cathode
