# Fritzing sketch id2909_electronica_1_0 (saved by Fritzing 0.9.3b)
breadboards: 1

parts:
  D2 = Rectifier Diode [part_number=1N4001 package="300 mil [THT]"]
  V2 = DC Power [voltage=5]
  D1 = Rectifier Diode [part_number=1N4001 package="300 mil [THT]"]
  R1 = Resistor [tolerance=±5% resistance=1k package="1206 [SMD]"]
  V1 = DC Power [voltage=5]
  R2 = Resistor [tolerance=±5% resistance=1k package=THT]

nets:
  N1: D2.cathode, R2.Pin_1
  N2: D2.anode, V2.V-
  N3: V2.V+, R2.Pin_0
  N4: D1.cathode, V1.V-
  N5: D1.anode, R1.Pin_0
  N6: R1.Pin_1, V1.V+
