# Fritzing sketch id290_Alarme_0 (saved by Fritzing 0.7.12b)

parts:
  Pir0 = screw terminal, 3 pins
  Pir1 = screw terminal, 3 pins
  Pir2 = screw terminal, 3 pins
  Pir3 = screw terminal, 3 pins
  Pir5 = screw terminal, 3 pins
  Pir4 = screw terminal, 3 pins
  Pir6 = screw terminal, 3 pins
  Pir7 = screw terminal, 3 pins
  GabrielRF = Arduino Prototyping Shield
  Diodo = Rectifier Diode [part_number=1N4001 package="300 mil [THT]"]
  560 = Resistor [tolerance=±5% resistance=220 package=THT]
  Transistor = NPN-Transistor [package="TO92 [THT]"]
  560_2 = Resistor [tolerance=±5% resistance=220 package=THT]
  12V = Power plug
  Buzina = Screw terminal - 2 pins [package=THT]

nets:
  N1: Pir0.pin1, Pir1.pin1, Pir2.pin1, Pir3.pin1, Pir5.pin1, Pir4.pin1, Pir6.pin1, Pir7.pin1, GabrielRF.+5V
  N2: Pir0.pin2, GabrielRF.D0(RX)
  GND: Pir0.pin3, Pir1.pin3, Pir2.pin3, Pir3.pin3, Pir5.pin3, Pir4.pin3, Pir6.pin3, Pir7.pin3, GabrielRF.GND, 560_2.Pin_1, 12V.GND, Buzina.pin2
  N3: Pir1.pin2, GabrielRF.D1(TX)
  N4: Pir2.pin2, GabrielRF.D4
  N5: Pir3.pin2, GabrielRF.D5
  N6: Pir5.pin2, GabrielRF.D7
  N7: Pir4.pin2, GabrielRF.D6
  N8: Pir6.pin2, GabrielRF.D8
  N9: Pir7.pin2, GabrielRF.D9
  N10: GabrielRF.D10, Diodo.anode
  N11: Diodo.cathode, 560.Pin_1
  N12: 560.Pin_0, Transistor.B
  N13: Transistor.E, 12V.VCC
  N14: Transistor.C, 560_2.Pin_0, Buzina.pin1

notes:
  gabrielferreira@ieee.org
  +
  0
  1
  2
  3
  4
  5
  6
  7
  8
  9
