# Fritzing sketch id2910_PCBgoodie_0 (saved by Fritzing 0.8.3b)
circuit board: 6.88561cm x 5.36311cm

parts:
  R1 = Resistor [tolerance=±5% resistance=220 package=THT]
  R2 = Resistor [tolerance=±5% resistance=220 package=THT]
  R3 = Resistor [tolerance=±5% resistance=220 package=THT]
  J1 = female pin header, 6 pins [form="♀ (female)"]
  J2 = female pin header, 6 pins [form="♀ (female)"]
  S1 = Toggle Switch [package=THT]
  S2 = Toggle Switch [package=THT]
  S3 = Toggle Switch [package=THT]
  part = Triple Axis Accelerometer Breakout - ADXL335
  LED = RGB LED (com. anode, rbg) [package="5 mm [THT]"]
  J3 = male pin header, 6 pins [form="♂ (male)"]
  J13 = female pin header, 14 pins [form="♀ (female)"]
  J11 = female pin header, 14 pins [form="♀ (female)"]
  Bauteil2 = Arduino Uno (Rev3)

nets:
  N1: R1.Pin_0, S1.L2
  N2: R1.Pin_1, LED.red_cathode
  N3: R2.Pin_0, S2.L2
  N4: R2.Pin_1, LED.blue_cathode
  N5: R3.Pin_0, S3.L2
  N6: R3.Pin_1, LED.green_cathode
  N7: J1.pin1, J1.pin2, J1.pin3, J1.pin4, J1.pin5, J1.pin6, Bauteil2.5V
  N8: J2.pin1, S3.COM, Bauteil2.A0
  N9: J2.pin2, S2.COM, Bauteil2.A1
  N10: J2.pin3, S1.COM, Bauteil2.A2
  N11: J2.pin4, Bauteil2.A3
  N12: J2.pin5, Bauteil2.A4/SDA
  N13: J2.pin6, Bauteil2.A5/SCL
  N14: S1.L1, part.XOUT
  N15: S2.L1, part.YOUT
  N16: S3.L1, part.ZOUT
  GND: part.GND, LED.common_anode, J3.pin1, J3.pin2, J3.pin3, J3.pin4, J3.pin5, J3.pin6, J11.pin1, J11.pin2, J11.pin3, J11.pin4, J11.pin5, J11.pin6, J11.pin7, J11.pin8, J11.pin9, J11.pin10, J11.pin11, J11.pin12, J11.pin13, J11.pin14, Bauteil2.GND
  VCC: part.VCC, Bauteil2.3V3
  N17: J13.pin1, Bauteil2.D13/SCK
  N18: J13.pin2, Bauteil2.D12/MISO
  N19: J13.pin3, Bauteil2.D11_PWM/MOSI
  N20: J13.pin4, Bauteil2.D10_PWM/SS
  N21: J13.pin5, Bauteil2.D9_PWM
  N22: J13.pin6, Bauteil2.D8
  N23: J13.pin7, Bauteil2.D7
  N24: J13.pin8, Bauteil2.D6_PWM
  N25: J13.pin9, Bauteil2.D5_PWM
  N26: J13.pin10, Bauteil2.D4
  N27: J13.pin11, Bauteil2.D3_PWM
  N28: J13.pin12, Bauteil2.D2
  N29: J13.pin13, Bauteil2.D1/TX
  N30: J13.pin14, Bauteil2.D0/RX

notes:
  Digital in
  GND
  0
  1
  2
  3
  9
  11
  4
  7
  8
  10
  12
  13
  5
  6
  5V
  Analog in
  x out
  y out
  z out
