# Fritzing sketch id2911_Module_LDR (saved by Fritzing 0.5.2b)
breadboards: 1

parts:
  LDR = Photocell (LDR) [package=THT]
  R1 = Resistor [resistance=10k package=THT]
  J1 = female pin header, 3 pins [form="♀ (female)"]

nets:
  N1: LDR.pin_0, R1.Pin_1, J1.pin2
  N2: LDR.pin_1, J1.pin3
  N3: R1.Pin_0, J1.pin1

notes:
  Module LDR, à utiliser avec arduino.
  Exemple sur :
  http://blog.crdp-versailles.fr/technogalois/index.php/category/Arduino,-modules-et-fonctions-associées
