# Fritzing sketch id2911_PCFan_Sample_01_0 (saved by Fritzing 0.9.3b)
breadboards: 1

parts:
  パーツ1 = Arduino Uno (Rev3)
  Q1 = MOSFET-NCHANNEL [package=to220v]
  M1 = DC Motor

nets:
  N1: パーツ1.GND, Q1.S
  N2: パーツ1.D3_PWM, Q1.G
  N3: パーツ1.VIN, M1.pin_2
  N4: Q1.D, M1.pin_1
