# Fritzing sketch id2912_Pedal_1_0 (saved by Fritzing 0.9.3b)
breadboards: 1

parts:
  BAT1 = BC9VPC [package=bc9vpc]
  U1 = 3.5mm Audio Jack [package=audio-jack-3.5mm-smd]
  U2 = 3.5mm Audio Jack [package=audio-jack-3.5mm-smd]
  R1 = Rotary Potentiometer (Small) [maximum_resistance=100kΩ package=THT]
  C1 = Ceramic Capacitor [capacitance=100nF package="100 mil [THT, multilayer]"]
  C2 = Ceramic Capacitor [capacitance=100nF package="100 mil [THT, multilayer]"]
  Q1 = NPN-Transistor [package="TO92 [THT]"]
  R22 = Resistor [tolerance=±10% resistance=100k package=THT]
  R23 = Resistor [tolerance=±5% resistance=1M package=THT]
  R24 = Resistor [tolerance=±5% resistance=1M package=THT]
  R25 = Resistor [tolerance=±0.5% resistance=10k package=THT]
  R29 = Resistor [tolerance=±5% resistance=390k package=THT]

nets:
  N1: BAT1.V+, R23.Pin_1, R25.Pin_1
  N2: BAT1.V-, U1.SLEEVE, U2.SLEEVE, R1.leg1, R22.Pin_1, R24.Pin_1, R29.Pin_0
  N3: U1.RIGHT, C1.1, R24.Pin_0
  N4: U2.RIGHT, R1.wiper
  N5: R1.leg2, C2.0
  N6: C1.0, Q1.B, R22.Pin_0, R23.Pin_0
  N7: C2.1, Q1.E
  N8: Q1.C, R29.Pin_1
