# Fritzing sketch id2913_PDuino_Control_Board_0.2x_0 (saved by Fritzing 0.8.5b)
circuit board: 5.57cm x 1.8cm
breadboards: 1

parts:
  R1 = Resistor [tolerance=±5% resistance=22k package=THT]
  R2 = Resistor [tolerance=±5% resistance=10k package=THT]
  R3 = Resistor [tolerance=±5% resistance=4.7k package=THT]
  R4 = Resistor [tolerance=±5% resistance=2.2k package=THT]
  S1 = Pushbutton [package="[THT]"]
  S2 = Pushbutton [package="[THT]"]
  S3 = Pushbutton [package="[THT]"]
  R5 = Resistor [tolerance=±5% resistance=4.7k package=THT]
  S4 = Pushbutton [package="[THT]"]
  DC_IN = DC Power [voltage=3.3V]
  J2 = male pin header, 5 pins [form="♂ (male)"]
  J1 = male pin header, 3 pins [form="♂ (male)"]
  J3 = male pin header, 5 pins [form="♂ (male)"]

nets:
  GND: R1.Pin_0, R2.Pin_0, R3.Pin_0, R4.Pin_0, J1.pin1
  N1: R1.Pin_1, S1.Pin_3, S1.Pin_4
  N2: R2.Pin_1, S2.Pin_3, S2.Pin_4
  N3: R3.Pin_1, S3.Pin_3, S3.Pin_4
  N4: R4.Pin_1, S4.Pin_3, S4.Pin_4
  N5: S1.Pin_1, S1.Pin_2, S2.Pin_1, S2.Pin_2, S3.Pin_1, S3.Pin_2, R5.Pin_1, S4.Pin_1, S4.Pin_2, J1.pin2
  N6: R5.Pin_0, DC_IN.V-, J1.pin3
  N7: J2.pin1, J3.pin1
  N8: J2.pin2, J3.pin2
  N9: J2.pin3, J3.pin3
  N10: J2.pin4, J3.pin4
  N11: J2.pin5, J3.pin5

notes:
  I/O
  GND
  RES
  RX
  TX
  +5V
  PDuino 0.2x
  +3.3V
