# Fritzing sketch id2914_PDuino_Power_Supply_0.31x_0 (saved by Fritzing 0.8.5b)
circuit board: 5.6cm x 4.4cm
breadboards: 1

parts:
  Fuse_(3A_slow) = Fuse with Handler [part_number="3A slow-blow fuse"]
  R3 = Resistor [tolerance=±5% resistance=100k package=THT]
  D3 = Rectifier Diode [part_number=1N4001 package="300 mil [THT]"]
  R4 = Resistor [tolerance=±5% resistance=47k package=THT]
  D4 = Zener Diode [part_number=5,6V breakdown_voltage=5.1V package="300 mil [THT]"]
  U2 = Voltage Regulator - 5V [part_number=LM2940CT-5 package="TO220 [THT]"]
  C5 = Electrolytic Capacitor [capacitance=47µF voltage=10V part_number="16V max." package="100 mil [THT, electrolytic]"]
  C6 = Ceramic Capacitor [capacitance=100nF package="200 mil [THT, multilayer]"]
  J3 = Screw terminal - 2 pins [part_number="To Arduino" package=THT]
  J4 = screw terminal, 2 pins
  J5 = male pin header, 1 pin [form="♂ (male)"]
  C4 = Electrolytic Capacitor [capacitance=4.7mF voltage=50V part_number="63V if avail." package="300 mil [THT, electrolytic]"]

nets:
  N1: Fuse_(3A_slow).Connector1, J4.pin2
  N2: Fuse_(3A_slow).Connector2, R3.Pin_0, D3.anode
  N3: R3.Pin_1, R4.Pin_0, D4.cathode, J5.pin1
  N4: D3.cathode, U2.input_voltage, C4.+
  N5: R4.Pin_1, D4.anode, U2.GND, C5.-, C6.0, J3.pin2, J4.pin1, C4.-
  N6: U2.output_voltage, C5.+, C6.1, J3.pin1

notes:
  "The other thing that is a little bit unusual about our power supply circuit is that we’ve deviated from the typical reference design by fitting an enormous capacitor across the voltage regulator input and feeding the input through a power diode. We’ve also included a voltage divider in front of the power diode and a Zener diode to act as a voltage clamp on the bottom of the divider.
  The reason for doing this is to give the Arduino the ability to elegantly handle power failure. Having a very large capacitor on the input of the voltage regulator provides enough reserve power to keep the voltage regulator running at its rated voltage for a few extra milliseconds after power is disconnected from the input. By having the CPU detect input failure through the voltage divider, it can use that time to quickly put its house in order before the power drops out entirely. Tasks it might need to do in that time include closing any files that are open on the USB memory stick, because if the power fails while a file is open it probably won’t be written properly and could end up corrupted or even entirely empty with all your logged data gone forever."
  "In order to detect power loss, the Arduino needs an input from the unregulated (+12V) side of the power-supply circuit. The input needs to change state fast enough for it to be detected and necessary action taken before the large capacitor on the input has time to discharge below the voltage regulator’s minimum stable input voltage of about 5.5V. Because the electrical system of a car can be very “noisy” with spikes and transient voltages, it’s a good idea to keep the Arduino on the regulated side of the circuit as decoupled from the input side of the power supply as possible. To achieve power-supply sensing, we used a pair of resistors as a voltage divider and a Zener diode as a voltage clamp with the output connected to a digital input on the Arduino.
  The voltage divider connects directly in front of the power diode so that it samples the voltage being supplied to it. If the input voltage falls, the voltage divider will see the drop immediately, even though the large capacitor on the voltage regulator input will remain high for a while. The diode prevents the capacitor from discharging back through the voltage divider and vehicle wiring loom and fooling the Arduino into thinking the input voltage is still normal until it’s too late.
  The voltage divider consists of a 100K upper half and a 47K lower half. The result is that the output of the voltage divider will be the input voltage times a factor of
  47 / (100 + 47) = 0.32
  So with a 12V input to the top of the divider, the output will be
  12 × 0.32 = 3.84V
  With a 14V input, the output will be
  14 × 0.32 = 4.48V
  We can also work back the other way to figure out the threshold at which the input voltage causes the output to fall low enough for the Arduino to detect a “logic low” level and begin its emergency shutdown procedure. The upper threshold for an input low voltage on ATMega CPUs is 0.3 × supply voltage. So for a CPU running at 5V, the trigger point for an input to see a logic low is any voltage below 1.5V."
  -   +
  - +
  To Arduino
  DC In
  DC Out
  PDuino 0.31x
  Pin 3
