# Fritzing sketch id2915_Traffic_light_sketch_0 (saved by Fritzing 0.9.3b)
breadboards: 1

parts:
  Part1 = Arduino Uno (Rev3)
  S1 = Pushbutton [package="[THT]"]
  R1 = Resistor [tolerance=±5% resistance=220 package=THT]
  R2 = Resistor [tolerance=±5% resistance=220 package=THT]
  R3 = Resistor [tolerance=±5% resistance=220 package=THT]
  LED1 = smd LED [color="Red (633nm)" package="0805 [SMD]"]
  LED2 = smd LED [color="Green (565nm)" package="0805 [SMD]"]
  LED3 = smd LED [color="Orange (612nm)" package="0805 [SMD]"]
  LED4 = smd LED [color="Red (633nm)" package="0805 [SMD]"]
  LED5 = smd LED [color="Orange (612nm)" package="0805 [SMD]"]
  LED6 = smd LED [color="Green (565nm)" package="0805 [SMD]"]
  R4 = Resistor [tolerance=±5% resistance=220 package=THT]
  R5 = Resistor [tolerance=±5% resistance=220 package=THT]
  R6 = Resistor [tolerance=±5% resistance=220 package=THT]
  R7 = Resistor [tolerance=±5% resistance=10k package="2512 [SMD]"]

nets:
  N1: Part1.D8, R3.Pin_1
  N2: Part1.D9_PWM, R2.Pin_1
  N3: Part1.D10_PWM/SS, R1.Pin_1
  N4: Part1.D11_PWM/MOSI, R6.Pin_1
  N5: Part1.D12/MISO, R5.Pin_1
  N6: Part1.D13/SCK, R4.Pin_1
  N7: Part1.D4, S1.Pin_1, S1.Pin_2, R7.Pin_0
  N8: Part1.5V, S1.Pin_3, S1.Pin_4
  N9: Part1.GND, LED1.cathode, LED2.cathode, LED3.cathode, LED4.cathode, LED5.cathode, LED6.cathode, R7.Pin_1
  N10: R1.Pin_0, LED1.anode
  N11: R2.Pin_0, LED3.anode
  N12: R3.Pin_0, LED2.anode
  N13: LED4.anode, R4.Pin_0
  N14: LED5.anode, R5.Pin_0
  N15: LED6.anode, R6.Pin_0
