# Fritzing sketch id2916_Audio_Volume (saved by Fritzing 0.5.2b)
breadboards: 1

parts:
  R1 = Rotary Potentiometer (Large) [package=THT]
  Output = Stereo Jack (TRS) 3.5mm [package="PG203J [THT]"]
  Input = Stereo Jack (TRS) 3.5mm [package="PG203J [THT]"]

nets:
  N1: R1.wiper, Output.Ring, Output.Tip
  N2: R1.leg2, Input.Ring, Input.Tip
  N3: Output.Sleeve, Input.Sleeve

notes:
  No connection on the bottom leg of the pot
  This is the most simple version. it will merge left and right, so if there is stero stuff going on it will get routed to both ears
