# Fritzing sketch id2916_Pegelstand2_0 (saved by Fritzing 0.9.3b)
circuit board: 5.17694cm x 5.33301cm
breadboards: 1

parts:
  Bauteil1 = Arduino Uno (Rev3)
  Ultraschall = longpad pin header, 4 pins [form="long pad"]
  TPL5110 = adafruit [part_number="Adafruit #3435"]
  R1 = Resistor [tolerance=±5% resistance=150k package=THT]
  Bauteil2 = verter_screw

nets (from the breadboard view):
  N1: Bauteil1.D12/MISO, TPL5110.connector10
  N2: Bauteil1.GND, Ultraschall.pin1, TPL5110.connector7, R1.Pin_0, Bauteil2.connector62
  N3: Bauteil1.D4, Ultraschall.pin2
  N4: Bauteil1.D5_PWM, Ultraschall.pin3
  N5: Bauteil1.5V, Ultraschall.pin4, TPL5110.connector9
  N6: TPL5110.connector6, Bauteil2.connector63
  N7: TPL5110.connector8, R1.Pin_1

notes:
  GND
  ECHO
  TRIGGER
  VCC
  5V IN
  5V OUT
  DELAY
  DONE
  5V
  3-12V IN
