# Fritzing sketch id291_Untitled_Sketch_3_0 (saved by Fritzing 0.9.3b)
breadboards: 1

parts:
  Componente1 = Arduino Uno (Rev3)
  C1 = Electrolytic Capacitor [capacitance=1µF package="100 mil [THT, electrolytic]"]
  S1 = Pushbutton [package="[THT]"]
  R1 = Resistor [tolerance=±5% resistance=220 package=THT]
  R2 = Rotary Potentiometer (Small) [maximum_resistance=100kΩ package=THT]
  R3 = Photocell (LDR) [package=THT]
  R4 = Resistor [tolerance=±5% resistance=10k package=THT]
  U1 = Voltage Regulator - 5V [package="TO220 [THT]"]
  U2 = RELAY [package=relay-jzc]
  Q1 = NPN-Transistor [package="TO92 [THT]"]
  R5 = Resistor [tolerance=±5% resistance=1k package=THT]
  J1 = Piezo Speaker
  D1 = Rectifier Diode [package="Melf DO-213 AA [SMD]"]  # not connected

nets:
  N1: Componente1.A0, R3.pin_1, R4.Pin_0
  N2: Componente1.A1, R2.wiper
  N3: Componente1.D10_PWM/SS, S1.Pin_1, R1.Pin_0
  N4: Componente1.D13/SCK, R5.Pin_1
  N5: Componente1.5V, C1.+, S1.Pin_3, S1.Pin_4, R2.leg1, R3.pin_0, U2.NC, U2.COIL1
  N6: Componente1.GND, R1.Pin_1, R2.leg2, R4.Pin_1, Q1.C, J1.pin1
  N7: C1.-, U1.GND
  N8: U2.NO, J1.pin2
  N9: U2.MAIN, Q1.E
  N10: Q1.B, R5.Pin_0
