# Fritzing sketch id2929_Yi's_Remote_Controller_0 (saved by Fritzing 0.9.0b)
breadboards: 1

parts:
  元件1 = Arduino BT
  D1 = SOLAR-IXYS [package=solarbit-12x1]
  元件2 = Lilypad Power Supply
  MIC1 = Microphone
  U1 = CAPSENSE_PAD [package=capsense_pad]
  U2 = CAPSENSE_PAD [package=capsense_pad]
  U3 = POT [package=pot_mammoth]
  LED1 = smd LED [color="Red (633nm)" package="1206 [SMD]"]
  R1 = Resistor [tolerance=±5% resistance=220 package="0805 [SMD]"]
  S1 = SWITCH-MOMENTARY-2 [package=tactile-pth]
  S2 = SWITCH-MOMENTARY-2 [package=tactile-pth]

nets:
  GND: 元件1.GND, D1.C, 元件2.GND, MIC1.pin1, U3.S, LED1.cathode, S1.1
  N1: 元件1.A5/SCL, 元件1.A5, U3.A
  N2: 元件1.A0, MIC1.pin2
  N3: 元件1.A1, U1.RES
  N4: 元件1.A2, U2.RES
  N5: 元件1.A3, S2.1
  N6: 元件1.A4, S1.2
  N7: 元件1.RESET_WT11/D7, R1.Pin_1
  N8: 元件1.5V, D1.A, 元件2.+, U3.E
  N9: U1.RECEIVE, U2.RECEIVE
  N10: LED1.anode, R1.Pin_0
