# Fritzing sketch id292_Alea_64_0 (saved by Fritzing 0.8.5b)
circuit board: 7.0612cm x 4.14468cm
breadboards: 1

parts:
  Teensy2 = Teensy 2.0
  HCF_2 = HCF 4067 [package="DIP24 [THT]"]
  J2 = female pin header, 14 pins [form="♀ (female)"]
  J3 = female pin header, 14 pins [form="♀ (female)"]
  J4 = female pin header, 18 pins [form="♀ (female)"]
  J5 = female pin header, 18 pins [form="♀ (female)"]

nets:
  N1: Teensy2.GND, Teensy2.B2, Teensy2.B3, HCF_2.12_VSS, HCF_2.13_D, HCF_2.14_C, J3.pin1, J3.pin2, J3.pin3, J3.pin4, J3.pin5, J3.pin6, J3.pin7, J3.pin8, J3.pin9, J3.pin10, J3.pin11, J3.pin12, J3.pin13, J3.pin14, J4.pin1, J4.pin2, J4.pin3, J4.pin4, J4.pin5, J4.pin6, J4.pin7, J4.pin8, J4.pin9, J4.pin10, J4.pin11, J4.pin12, J4.pin13, J4.pin14, J4.pin15, J4.pin16, J4.pin17, J4.pin18
  N2: Teensy2.B0, HCF_2.10_A
  N3: Teensy2.B1, HCF_2.11_B
  N4: Teensy2.B7, Teensy2.C7, HCF_2.1_O/I, J2.pin6
  N5: Teensy2.D0, J2.pin1
  N6: Teensy2.D1, J2.pin2
  N7: Teensy2.D2, J2.pin3
  N8: Teensy2.D3, J2.pin4
  N9: Teensy2.C6, J2.pin5
  N10: Teensy2.VCC, Teensy2.D6, HCF_2.24_Vdd, J5.pin11
  N11: Teensy2.D7, J5.pin10
  N12: Teensy2.B4, J5.pin9
  N13: Teensy2.B5, J5.pin8
  N14: Teensy2.B6, J5.pin7
  N15: Teensy2.F7, J5.pin6
  N16: Teensy2.F6, J5.pin5
  N17: Teensy2.F5, J5.pin4
  N18: Teensy2.F4, J5.pin3
  N19: Teensy2.F1, J5.pin2
  N20: Teensy2.F0, J5.pin1
  N21: HCF_2.2_TG_7, J2.pin7
  N22: HCF_2.3_TG6, J2.pin8
  N23: HCF_2.4_TG5, J2.pin9
  N24: HCF_2.5_TG4, J2.pin10
  N25: HCF_2.6_TG3, J2.pin11
  N26: HCF_2.7_TG2, J2.pin12
  N27: HCF_2.8_TG1, J2.pin13
  N28: HCF_2.9_TG0, J2.pin14
  N29: HCF_2.17_TG14, J5.pin18
  N30: HCF_2.18_TG13, J5.pin17
  N31: HCF_2.19_TG12, J5.pin16
  N32: HCF_2.20_TG11, J5.pin15
  N33: HCF_2.21_TG10, J5.pin14
  N34: HCF_2.22_TG9, J5.pin13
  N35: HCF_2.23_TG8, J5.pin12
