# Fritzing sketch id2931_pf3fritzing_0 (saved by Fritzing 0.7.12b)
breadboards: 1

parts:
  Arduino1 = Arduino
  R1 = Basic Flex Resistor
  S2 = Round Pushbutton
  R3 = 10k Ω Resistor [package=THT]
  R2 = 33k Ω Resistor [package=THT]

nets:
  N1: Arduino1.D2, S2.leg0, R3.Pin_1
  N2: Arduino1.+5V, R1.Pin_2, S2.leg1
  N3: Arduino1.GND, R3.Pin_0, R2.Pin_0
  N4: Arduino1.A0, R1.pin_1, R2.Pin_1

notes:
  Flexsensor har en 33kOhm modstand
  Den hjemmelavede knap har en 10kOhm modstand
