# Fritzing sketch id2932_pH_Corrector_v2.0_0 (saved by Fritzing 0.8.7b)
circuit board: 6.88566cm x 5.36311cm
breadboards: 1

parts:
  D1 = Rectifier Diode [part_number=1N4001 package="300 mil [THT]"]
  Q1 = NPN-Transistor [package="TO92 [THT]"]
  Q2 = NPN-Transistor [package="TO92 [THT]"]
  R2 = Resistor [tolerance=±5% resistance=1k package=THT]
  R3 = Resistor [tolerance=±5% resistance=1k package=THT]
  C2 = Ceramic Capacitor [capacitance=0.1mF package="200 mil [THT, multilayer]"]
  C1 = Ceramic Capacitor [capacitance=0.1mF package="200 mil [THT, multilayer]"]
  S2 = Pushbutton [package="[THT]"]
  S3 = Pushbutton [package="[THT]"]
  S4 = Pushbutton [package="[THT]"]
  R4 = Resistor [tolerance=±5% resistance=10k package=THT]
  R5 = Resistor [tolerance=±5% resistance=10k package=THT]
  R6 = Resistor [tolerance=±5% resistance=10k package=THT]
  S1 = Pushbutton [package="[THT]"]
  D2 = Rectifier Diode [part_number=1N4001 breakdown_voltage=3.6V package="300 mil [THT]"]
  J15 = screw terminal, 4 pins
  J8 = double row female pin header, 14 pins [form="♀ (female)"]
  U1 = BNC [package=bnc]
  pH_Circuit1 = pH Circuit
  R7 = Resistor [tolerance=±5% resistance=10k package=THT]
  Часть1 = Arduino Uno (Rev3)
  M1 = DC Motor
  M2 = DC Motor
  LCD1 = LCD screen

nets:
  N1: D1.cathode, C2.0, C1.0, D2.cathode
  N2: D1.anode, Q1.E, C1.1, J15.pin2, M2.pin_1
  N3: Q1.B, R3.Pin_1
  GND: Q1.C, Q2.C, R4.Pin_1, R5.Pin_1, R6.Pin_1, J8.pin8, J8.pin9, J8.pin10, pH_Circuit1.GND#0, R7.Pin_1, Часть1.GND, LCD1.VSS, LCD1.V0, LCD1.R/W
  N4: Q2.E, C2.1, D2.anode, J15.pin4, M1.pin_1
  N5: Q2.B, R2.Pin_0
  N6: R2.Pin_1, Часть1.D6_PWM
  N7: R3.Pin_0, Часть1.D7
  VCC: S2.Pin_1, S2.Pin_2, S3.Pin_1, S3.Pin_2, S4.Pin_1, S4.Pin_2, S1.Pin_1, S1.Pin_2, J8.pin7, pH_Circuit1.Vcc, Часть1.5V, LCD1.VDD
  N8: S2.Pin_3, S2.Pin_4, R6.Pin_0, Часть1.A2
  N9: S3.Pin_3, S3.Pin_4, R5.Pin_0, Часть1.A1
  N10: S4.Pin_3, S4.Pin_4, R4.Pin_0, Часть1.A0
  N11: S1.Pin_3, S1.Pin_4, R7.Pin_0, Часть1.A3
  N12: J15.pin1, J15.pin3, Часть1.VIN, M1.pin_2, M2.pin_2
  N13: J8.pin1, Часть1.D13/SCK, LCD1.DB7
  N14: J8.pin2, Часть1.D11_PWM/MOSI, LCD1.DB5
  N15: J8.pin5, Часть1.D9_PWM, LCD1.E
  N16: J8.pin6, Часть1.D8, LCD1.RS
  N17: J8.pin13, Часть1.D10_PWM/SS, LCD1.DB4
  N18: J8.pin14, Часть1.D12/MISO, LCD1.DB6
  N19: U1.GND, pH_Circuit1.GND#5
  N20: U1.OUT, pH_Circuit1.PRB
  N21: pH_Circuit1.TX, Часть1.D5_PWM
  N22: pH_Circuit1.RX, Часть1.D3_PWM

notes:
  pH Corrector Shield v2.5
  CyberPlant
  GND
  Vin
  http://cyberplant.info
  peristaltic pump pH Up
  peristaltic pump pH Down
