# Fritzing sketch id2933_PS+48V_0 (saved by Fritzing 0.9.2b)
circuit board: 5.40087cm x 2.96655cm
breadboards: 1

parts:
  V1 = DC Power [voltage=12V]
  D1 = Diode [part_number=DFLS1100-7 package=diode-1n4148]
  C1 = Electrolytic Capacitor [capacitance=100µF voltage=20V package="300 mil [THT, electrolytic]"]
  U1 = LM2585
  R1 = Resistor [tolerance=±5% resistance=2.4k package=THT]
  C3 = Ceramic Capacitor [capacitance=0.47µF package="200 mil [THT, multilayer]"]
  R2 = Resistor [tolerance=±5% resistance=57.6k package=THT]
  R3 = Resistor [tolerance=±5% resistance=1.5k package=THT]
  C2 = Ceramic Capacitor [capacitance=1µF package="200 mil [THT, multilayer]"]
  C4 = Electrolytic Capacitor [capacitance=47µF voltage=63V package="300 mil [THT, electrolytic]"]
  L1 = Inductor [inductance=1mH part_number=PM2110-102K-RC package="400 mil [THT]"]
  D2 = LTE-302 [package=lte-302]
  R4 = Resistor [tolerance=±5% resistance=47k package=THT]

nets:
  N1: V1.V+, C1.+, U1.connector4, C2.1, L1.pin_0
  GND: V1.V-, C1.-, U1.connector2, U1.connector5, C3.0, R3.Pin_1, C2.0, C4.-, D2.C
  N2: D1.A, U1.connector3, L1.pin_1
  N3: D1.C, R2.Pin_0, C4.+, R4.Pin_0
  N4: U1.connector0, R1.Pin_0
  N5: U1.connector1, R2.Pin_1, R3.Pin_0
  N6: R1.Pin_1, C3.1
  N7: D2.A, R4.Pin_1
