# Fritzing sketch id2934_PhotoResistor_0 (saved by Fritzing 0.8.7b)
breadboards: 1

parts:
  R1 = Resistor [tolerance=±5% resistance=10k package=THT]
  Part1 = Arduino Uno (Rev3)
  R2 = Photocell (LDR) [package=THT]
  R3 = Resistor [tolerance=±5% resistance=10k package=THT]
  LED1 = LED - 5mm [color="Red (633nm)" package="5 mm [THT]"]
  R4 = Resistor [tolerance=±5% resistance=10k package=THT]
  R5 = Resistor [tolerance=±5% resistance=220 package=THT]
  R6 = Resistor [tolerance=±5% resistance=220 package=THT]
  LED2 = LED - 5mm [color="Red (633nm)" package="5 mm [THT]"]
  LED3 = LED - 5mm [color="Green (560nm)" package="5 mm [THT]"]
  LED4 = LED - 5mm [color="Green (560nm)" package="5 mm [THT]"]
  LED5 = LED - 5mm [color="Blue (470nm)" package="5 mm [THT]"]
  R7 = Resistor [tolerance=±5% resistance=10k package=THT]

nets:
  N1: R1.Pin_0, Part1.A0, R2.pin_1
  N2: R1.Pin_1, Part1.GND, LED1.anode, LED3.anode, LED4.anode, LED5.anode
  N3: Part1.D2, R3.Pin_0
  N4: Part1.D3_PWM, R4.Pin_0
  N5: Part1.D4, R5.Pin_0
  N6: Part1.D5_PWM, R6.Pin_0
  N7: Part1.D6_PWM, R7.Pin_0
  N8: Part1.5V, R2.pin_0
  N9: R3.Pin_1, LED1.cathode
  N10: R4.Pin_1, LED2.cathode
  N11: R5.Pin_1, LED3.cathode
  N12: R6.Pin_1, LED4.cathode
  N13: LED5.cathode, R7.Pin_1
