# Fritzing sketch id2935_Photocell_onOff_0 (saved by Fritzing 0.9.3b)
breadboards: 1

parts:
  Part1 = Arduino Uno (Rev3)
  LED1 = LED - 5mm [color="Red (633nm)" package="5 mm [THT]"]
  R1 = Resistor [tolerance=±5% resistance=220 package=THT]
  R2 = Photocell (LDR) [package=THT]
  R3 = Resistor [tolerance=±5% resistance=220 package=THT]

nets:
  N1: Part1.A3, R2.pin_1, R3.Pin_0
  N2: Part1.D3_PWM, LED1.anode
  N3: Part1.5V, R2.pin_0
  N4: Part1.GND, R1.Pin_0, R3.Pin_1
  N5: LED1.cathode, R1.Pin_1

notes:
  LED connects to Pin 3
  Photocell connects to A3
  Resistors:
  LED 220Ω
  Photocell 10kΩ
