# Fritzing sketch id2936_Photocell_RGB_Servo_Piezo___Week_4_0 (saved by Fritzing 0.9.3b)
circuit board: 6.88566cm x 5.36311cm
breadboards: 1

parts:
  Arduino1 = Arduino Uno (Rev3)
  R6 = Resistor [tolerance=±5% resistance=10k package=THT]
  R8 = Photocell (LDR) [package=THT]
  R9 = Resistor [tolerance=±5% resistance=10k package=THT]
  R12 = Resistor [tolerance=±5% resistance=220 package=THT]
  R10 = Resistor [tolerance=±5% resistance=220 package=THT]
  LED1 = RGB LED (com. cathode, rbg) [package="5 mm [THT]"]
  R15 = Photocell (LDR) [package=THT]
  R16 = Photocell (LDR) [package=THT]
  J1 = Basic Servo
  J2 = Piezo Speaker
  R11 = Resistor [tolerance=±5% resistance=220 package=THT]
  R14 = Resistor [tolerance=±5% resistance=10k package=THT]

nets:
  N1: Arduino1.A0, R16.pin_0, R14.Pin_0
  N2: Arduino1.A1, R6.Pin_0, R15.pin_0
  N3: Arduino1.A2, R8.pin_0, R9.Pin_0
  N4: Arduino1.D8, J1.pulse
  N5: Arduino1.D9_PWM, R10.Pin_1
  N6: Arduino1.D10_PWM/SS, R11.Pin_1
  N7: Arduino1.D11_PWM/MOSI, R12.Pin_1
  GND: Arduino1.GND, R6.Pin_1, R9.Pin_1, LED1.common_cathode, J1.gnd, J2.pin1, R14.Pin_1
  N8: Arduino1.D3_PWM, J2.pin2
  5V: Arduino1.5V, R8.pin_1, R15.pin_1, R16.pin_1, J1.vcc
  N9: R12.Pin_0, LED1.red_anode
  N10: R10.Pin_0, LED1.green_anode
  N11: LED1.blue_anode, R11.Pin_0
