# Fritzing sketch id2937_teste_0 (saved by Fritzing 0.9.0b)
breadboards: 1

parts:
  Part1 = Arduino Uno (Rev3)
  C1 = Ceramic Capacitor [capacitance="100 nF" package="0603 [SMD, multilayer]"]
  LTC_1050 = LM386 [part_number="ltc 1050" package=dip08]
  R2 = Resistor [tolerance=±5% resistance=10k package="1206 [SMD]"]
  P1 = S1133 Si Photodiode [package="8mm Ceramic [THT]"]

nets:
  N1: Part1.A0, C1.1, LTC_1050.V+, R2.Pin_1
  N2: Part1.5V, LTC_1050.BP
  N3: Part1.GND, LTC_1050.V-
  N4: C1.0, R2.Pin_0
  N5: LTC_1050.-IN, P1.anode
  N6: LTC_1050.+IN, P1.cathode
