# Fritzing sketch id2938_bbq_0 (saved by Fritzing 0.9.2b)
breadboards: 1

parts:
  Part1 = Photon
  U1 = 2.5mm Audio Jack [package=stereojack2.5mm_stereojack2.5mm]
  J1 = Power Jack [package=power_jack_slot]
  U2 = 2.5mm Audio Jack [package=stereojack2.5mm_stereojack2.5mm]

nets:
  N1: Part1.A0, U1.SLEEVE
  N2: Part1.A1, U2.SLEEVE
  GND: Part1.GND, J1.GND
  N3: Part1.VIN, J1.PWR
