# Fritzing sketch id2940_temperature_photon_0 (saved by Fritzing 0.9.2b)
breadboards: 1

parts:
  R1 = Resistor [tolerance=±5% resistance=4.7k package=THT]
  T1 = DS18B20
  Part1 = Photon

nets:
  N1: R1.Pin_0, T1.connector2, Part1.3V3
  N2: R1.Pin_1, T1.connector1, Part1.D1
  N3: T1.connector0, Part1.GND
