# Fritzing sketch id2942_sams_physics_0 (saved by Fritzing 0.9.3b)
breadboards: 1

parts:
  Part1 = Arduino Ethernet Shield (Rev3)
  R1 = Resistor [tolerance=±5% resistance=220 package=THT]
  R2 = Resistor [tolerance=±5% resistance=220 package=THT]
  R3 = Resistor [tolerance=±5% resistance=220 package=THT]

nets:
  N1: Part1.TX/D1, R1.Pin_1
  N2: Part1.D2, R2.Pin_1
  N3: Part1.PWM_D3, R3.Pin_1
  N4: Part1.GND, R1.Pin_0, R2.Pin_0, R3.Pin_0
