# Fritzing sketch id2943_Untitled_Sketch_2_0 (saved by Fritzing 0.9.2b)
breadboards: 1

parts:
  Часть1 = Arduino Uno (Rev3)
  R1 = Resistor [tolerance=±5% resistance=220 package=THT]
  LED1 = LED - 5mm [color="Red (633nm)" package="5 mm [THT]"]
  R2 = Resistor [tolerance=±5% resistance=220 package=THT]
  LED2 = LED - 5mm [color="White (4500K)" package="5 mm [THT]"]
  S1 = Pushbutton [package="[THT]"]
  S2 = Pushbutton [package="[THT]"]
  R3 = Resistor [tolerance=±5% resistance=220 package=THT]
  R4 = Resistor [tolerance=±5% resistance=220 package=THT]

nets:
  N1: Часть1.D8, R2.Pin_1
  N2: Часть1.D12/MISO, R1.Pin_1
  N3: Часть1.GND, LED1.cathode, LED2.cathode, R3.Pin_1, R4.Pin_1
  N4: Часть1.D2, S1.Pin_1, S1.Pin_2, R4.Pin_0
  N5: Часть1.D4, S2.Pin_1, S2.Pin_2, R3.Pin_0
  N6: Часть1.5V, S1.Pin_3, S1.Pin_4, S2.Pin_3, S2.Pin_4
  N7: R1.Pin_0, LED1.anode
  N8: R2.Pin_0, LED2.anode
