# Fritzing sketch id2945_Clock_0 (saved by Fritzing 0.9.0b)
breadboards: 1

parts:
  7SEG1 = 7_Segment_LED_I2C_Backpack__blue
  OLED2 = 128x64_Monochrom_OLED_Display_with_SPI_Control
  BB1 = 4_Line_Bi_Directional_Level_Shifter
  Pi1 = Pi_Cobbler

nets:
  N1: 7SEG1.connector1, Pi1.connector2
  N2: 7SEG1.connector2, Pi1.connector6
  N3: 7SEG1.connector3, BB1.connector14
  N4: 7SEG1.connector4, BB1.connector15
  N5: OLED2.connector6, OLED2.connector7
  N6: BB1.connector1, Pi1.connector17
  N7: BB1.connector4, Pi1.connector3
  N8: BB1.connector5, Pi1.connector5
  N9: BB1.connector6, Pi1.connector25
