# Fritzing sketch id2946_Pi_Simple2_0 (saved by Fritzing 0.9.1b)
circuit board: 2.38816cm x 3.83995cm
breadboards: 1

parts:
  R1 = Resistor [tolerance=±5% resistance=220 package=THT]
  R2 = Resistor [tolerance=±5% resistance=220 package=THT]
  R3 = Resistor [tolerance=±5% resistance=220 package=THT]
  R4 = Resistor [tolerance=±5% resistance=220 package=THT]
  LED1 = LED - 5mm [color="Red (633nm)" package="5 mm [THT]"]
  LED2 = LED - 5mm [color="Yellow (592nm)" package="5 mm [THT]"]
  LED3 = LED - 5mm [color="Green (565nm)" package="5 mm [THT]"]
  LED4 = LED - 5mm [color="Blue (505nm)" package="5 mm [THT]"]
  U1 = mystery part, 3 pins [chip_label=ds1820]
  R5 = Resistor [tolerance=±5% resistance=4.7k package=THT]
  S1 = Pushbutton [package="[THT]"]
  J2 = rounded female pin header, 4 pins [form="♀ (female rounded)"]
  J3 = rounded female pin header, 13 pins [form="♀ (female rounded)"]
  R6 = Resistor [tolerance=±5% resistance=4.7k package=THT]

nets:
  N1: R1.Pin_0, J3.pin10
  N2: R1.Pin_1, LED1.anode
  N3: R2.Pin_0, J3.pin8
  N4: R2.Pin_1, LED2.anode
  N5: R3.Pin_0, J3.pin7
  N6: R3.Pin_1, LED3.anode
  N7: R4.Pin_0, J3.pin6
  N8: R4.Pin_1, LED4.anode
  N9: LED1.cathode, LED2.cathode, LED3.cathode, LED4.cathode, J2.pin1, J3.pin13
  N10: U1.pin1, J3.pin5
  N11: U1.pin2, R5.Pin_1, J3.pin4
  N12: U1.pin3, R5.Pin_0, J3.pin1
  N13: S1.Pin_2, J3.pin11
  N14: S1.Pin_3, S1.Pin_4, R6.Pin_1
  N15: J2.pin3, J3.pin2
  N16: J2.pin4, J3.pin3
  N17: J3.pin9, R6.Pin_0
