# Fritzing sketch id2948_RF_remote_0 (saved by Fritzing 0.9.0b)
perfboards: 1
stripboards: 1

parts:
  Raspberry_Pi1 = Raspberry Pi B rev2
  Q1 = NPN-Transistor [package="TO92 [THT]"]
  Q2 = NPN-Transistor [package="TO92 [THT]"]
  LED1 = LED - 5mm [color="Red (633nm)" package="5 mm [THT]"]  # not connected
  S1 = Pushbutton [package="[THT]"]
  S2 = Pushbutton [package="[THT]"]
  VCC1 = Battery
  R1 = Resistor [tolerance=±5% resistance=220 package=THT]
  R2 = Resistor [tolerance=±5% resistance=220 package=THT]

nets:
  N1: Raspberry_Pi1.3V3, VCC1.+
  N2: Raspberry_Pi1.GND, Q1.E, Q1.C, Q2.E, Q2.B, Q2.C, S1.Pin_3, S1.Pin_4, S2.Pin_3, S2.Pin_4, VCC1.-, R2.Pin_1
  N3: Raspberry_Pi1.GPIO_23, R2.Pin_0
  N4: Raspberry_Pi1.GPIO_24, R1.Pin_1
  N5: Q1.B, R1.Pin_0
  N6: S1.Pin_1, S1.Pin_2
  N7: S2.Pin_1, S2.Pin_2
