# Fritzing sketch id2949_servolu_kontrol_Pi_CAR_V3_0 (saved by Fritzing 0.9.3b)
breadboards: 1

parts:
  Raspberry_Pi_1 = Raspberry Pi 3 [part_number=RPI-3-V1.2]
  J2 = Basic Servo
  J3 = Basic Servo
  +12V_BATTERY = Battery Holders [package=lipo-1100mAh]
  J1 = Basic Servo
  LM2576_12V_TO_5V = RioRand LM2596
  +5V_VCC = 4 x AAA Battery Mount
  BTS7960_MOTOR_DRIVE = Header 2 [package=jst-2-pth-ns]
  L-R_PWM_||_L-R_ENABLE = Header 2 [package=jst-2-pth-ns]

nets:
  GND: Raspberry_Pi_1.GND, J2.gnd, J3.gnd, J1.gnd, LM2576_12V_TO_5V.Pin_3, +5V_VCC.-
  N1: Raspberry_Pi_1.GPIO17, J3.pulse
  N2: Raspberry_Pi_1.GPIO13, BTS7960_MOTOR_DRIVE.2
  N3: Raspberry_Pi_1.GPIO19, BTS7960_MOTOR_DRIVE.1
  N4: Raspberry_Pi_1.GPIO12, J1.pulse
  N5: Raspberry_Pi_1.GPIO24, L-R_PWM_||_L-R_ENABLE.1
  N6: Raspberry_Pi_1.GPIO23, L-R_PWM_||_L-R_ENABLE.2
  N7: Raspberry_Pi_1.GPIO18, J2.pulse
  N8: Raspberry_Pi_1.5V, +5V_VCC.+
  VCC: J2.vcc, J3.vcc, J1.vcc, LM2576_12V_TO_5V.Pin_2
  N9: +12V_BATTERY.+, LM2576_12V_TO_5V.Pin_1
  N10: +12V_BATTERY.-, LM2576_12V_TO_5V.Pin_0

notes:
  KAMERA DİKEY EKSEN
  HAREKET SERVOSU
  KAMERA YATAY EKSEN
  HAREKET SERVOSU
  DİREKSİYON YÖN KONTROL SERVOSU
