# Fritzing sketch id2950_PIANO_0 (saved by Fritzing 0.9.3b)
circuit board: 8.46667cm x 5.64444cm
breadboards: 1

parts:
  Součástka1 = Arduino Uno (Rev3)
  J1 = Piezo Speaker
  R1 = Resistor [tolerance=±5% resistance=10k package="0402 [SMD]"]
  S1 = Momentary Switch [package=ksa_sealed_tac_switch]
  R2 = Resistor [tolerance=±5% resistance=1M package="0603 [SMD]"]
  S2 = Momentary Switch [package=ksa_sealed_tac_switch]
  R3 = Resistor [tolerance=±5% resistance=10k package="0603 [SMD]"]
  S3 = Momentary Switch [package=ksa_sealed_tac_switch]
  R4 = Resistor [tolerance=±5% resistance=220 package="0603 [SMD]"]
  S4 = Momentary Switch [package=ksa_sealed_tac_switch]

nets:
  N1: Součástka1.A0, R1.Pin_1, S1.3, S2.3, S3.3, S4.3
  N2: Součástka1.D8, J1.pin1
  N3: Součástka1.GND, J1.pin2, R1.Pin_0
  N4: Součástka1.5V, R2.Pin_1, R3.Pin_1, R4.Pin_1, S4.1
  N5: S1.1, R2.Pin_0
  N6: S2.1, R3.Pin_0
  N7: S3.1, R4.Pin_0
