# Fritzing sketch id2951_dht22_0 (saved by Fritzing 0.9.3b)
breadboards: 1

parts:
  Raspberry_Pi1 = Raspberry Pi B rev2
  RHT1 = Humidity and Temperature Sensor RHT03
  R1 = Resistor [tolerance=±5% resistance=220 package="2512 [SMD]"]

nets:
  3V3: Raspberry_Pi1.3V3, RHT1.Vcc, R1.Pin_0
  N1: Raspberry_Pi1.GND, RHT1.GND_2
  N2: Raspberry_Pi1.GPIO_4, RHT1.Data-signal, R1.Pin_1
