# Fritzing sketch id2953_tempSensor_GroundFilled_0 (saved by Fritzing 0.9.1b)
circuit board: 6.23908cm x 4.04784cm
breadboards: 1

parts:
  PIC16 = PIC16F88-DIP [package=dil18]
  LM35 = LM35 Temperature Sensor [package="TO92 [THT]"]
  MAX485 = MAX485 [package=dil08]
  LM2594 = LM2594N [chip_label=LM2594]
  COUT = Electrolytic Capacitor [capacitance=100µF voltage=16V package="100 mil [THT, electrolytic]"]
  LOUT = Inductor [package="400 mil [THT]"]
  D1 = Schottky Diode [part_number=1N5817 package="300 mil [THT]"]
  VIN = Screw terminal - 2 pins [package=THT]
  CIN = Electrolytic Capacitor [capacitance=47µF voltage=25V package="100 mil [THT, electrolytic]"]
  RS485 = Screw terminal - 2 pins [package=THT]
  Sensors = FTDI_BASIC [package=ftdi_basic]
  R1 = Resistor [tolerance=±5% resistance=10k package=THT]
  ICSP = Header 6 [package=molex-1x6-ra]
  TX = LED - 3mm [color="Green (570nm)" package="3 mm [THT]"]
  R2 = Resistor [tolerance=±5% resistance=220 package=THT]
  LED = LED - 3mm [color="Red (633nm)" package="3 mm [THT]"]
  R3 = Resistor [tolerance=±5% resistance=220 package=THT]

nets:
  N1: PIC16.RA2_AN2, Sensors.5
  N2: PIC16.RA5_MCLR, R1.Pin_0, ICSP.1
  GND: PIC16.VSS, LM35.GND, MAX485.GND, LM2594.connector4, LM2594.connector5, COUT.-, D1.anode, VIN.pin1, CIN.-, Sensors.6, Sensors.3, ICSP.3, R2.Pin_1, LED.cathode
  N3: PIC16.RB1_SDA, MAX485.RO
  N4: PIC16.RB2_RX, MAX485.DI
  N5: PIC16.RB3, MAX485.RE, MAX485.DE, TX.anode
  N6: PIC16.RB4_SCL, R3.Pin_1
  N7: PIC16.RB6_PGC, ICSP.5
  N8: PIC16.RB7_PGD, ICSP.4
  VDD: PIC16.VDD, LM35.+Vs, MAX485.VCC, LM2594.connector3, COUT.+, LOUT.pin_0, Sensors.1, Sensors.4, R1.Pin_1, ICSP.2
  N9: PIC16.RA0_AN0, LM35.Vout
  N10: PIC16.RA1_AN1, Sensors.2
  N11: MAX485.A, RS485.pin2
  N12: MAX485.B, RS485.pin1
  N13: LM2594.connector6, VIN.pin2, CIN.+
  N14: LM2594.connector7, LOUT.pin_1, D1.cathode
  N15: TX.cathode, R2.Pin_0
  N16: LED.anode, R3.Pin_0

notes:
  A B
  + -
  + s1 - + s2 -
  ICSP
  1  2  3  4  5  6
  GRAAL
  2015
  Lab
  OrTo
  SensOrTo
  485
