# Fritzing sketch id2954_chip_up_the_right_way_from_the_start_basic_with_routing_and_pcb_layout_0 (saved by Fritzing 0.9.3b)
circuit board: 14.8769cm x 6.73645cm
breadboards: 1

parts:
  IC1 = PICAXE-08 [package=THT]
  R1 = Resistor [tolerance=±5% resistance=22k package=THT]
  R2 = Resistor [tolerance=±5% resistance=10k package=THT]
  VCC1 = 4 x AAA Battery Mount

nets:
  N1: IC1.+V, VCC1.+
  N2: IC1.Serial_In, R1.Pin_1
  N3: IC1.0V, R2.Pin_0, VCC1.-
  N4: R1.Pin_0, R2.Pin_1
