# Fritzing sketch id2955_H_bridge_dc_motor_driver_ (saved by Fritzing 0.3.14b)
breadboards: 1

parts:
  QP = PNP-Transistor [package="TO92 [THT]"]
  QN = NPN-Transistor [package="TO92 [THT]"]
  QN_2 = NPN-Transistor [package="TO92 [THT]"]
  QN_3 = NPN-Transistor [package="TO92 [THT]"]
  QN_4 = NPN-Transistor [package="TO92 [THT]"]
  QP_2 = PNP-Transistor [package="TO92 [THT]"]
  QP_3 = PNP-Transistor [package="TO92 [THT]"]
  QN_5 = NPN-Transistor [package="TO92 [THT]"]
  QN_6 = NPN-Transistor [package="TO92 [THT]"]
  QN_7 = NPN-Transistor [package="TO92 [THT]"]
  QN_8 = NPN-Transistor [package="TO92 [THT]"]
  M2 = DC Motor
  M1 = DC Motor
  R1 = Resistor [resistance=100k package=THT]
  R1_2 = Resistor [resistance=100k package=THT]
  R1_3 = Resistor [resistance=100k package=THT]
  R1_4 = Resistor [resistance=100k package=THT]
  QP_4 = PNP-Transistor [package="TO92 [THT]"]
  V+ = obsolete Battery
  D = Rectifier Diode [package=THT]
  QN_9 = Arduino
  D_2 = Rectifier Diode [package=THT]
  D_3 = Rectifier Diode [package=THT]
  D_4 = Rectifier Diode [package=THT]
  R2 = Resistor [resistance=220 package=THT]
  R2_2 = Resistor [resistance=220 package=THT]
  R2_3 = Resistor [resistance=220 package=THT]
  R2_4 = Resistor [resistance=220 package=THT]

nets:
  N1: QP.E, QP_2.E, QP_3.E, QP_4.E, V+.+, QN_9.VIN
  N2: QP.B, R2.Pin_0
  N3: QP.C, QN_2.C, M1.pin_2, D_4.cathode
  N4: QN.E, QN_4.B
  N5: QN.B, R1.Pin_1, D_4.anode
  N6: QN.C, R2.Pin_1
  N7: QN_2.E, QN_4.E, QN_7.E, QN_8.E, V+.-, QN_9.GND
  N8: QN_2.B, QN_3.E
  N9: QN_3.B, R1_2.Pin_1, D.anode
  N10: QN_3.C, R2_2.Pin_1
  N11: QN_4.C, M1.pin_1, QP_4.C, D.cathode
  N12: QP_2.B, R2_3.Pin_0
  N13: QP_2.C, QN_8.C, M2.pin_2, D_3.cathode
  N14: QP_3.B, R2_4.Pin_0
  N15: QP_3.C, QN_7.C, M2.pin_1, D_2.cathode
  N16: QN_5.E, QN_7.B
  N17: QN_5.B, R1_3.Pin_1, D_3.anode
  N18: QN_5.C, R2_3.Pin_1
  N19: QN_6.E, QN_8.B
  N20: QN_6.B, R1_4.Pin_0, D_2.anode
  N21: QN_6.C, R2_4.Pin_1
  N22: R1.Pin_0, QN_9.D11
  N23: R1_2.Pin_0, QN_9.D10
  N24: R1_3.Pin_0, QN_9.D6
  N25: R1_4.Pin_1, QN_9.D5
  N26: QP_4.B, R2_2.Pin_0

notes:
  This is a dual motor driver made out of transistors resistors and diodes. You should be able to find these components at local stores, opposed to having to buy motor driver IC's online.
  The components can be different, but my knowledge is limited so I will only recomend the ones I used.
  Components I used.
  4x PNP Transistors - 2N3906 type
  8x NPN Transistors - 2N3904 type
  4x Silicon Diodes - IN4001
  4x 100kΩ Resistors
  4x 220Ω Resistors
  I bought all from local Radioshack stores
  GND
