# Fritzing sketch id2955_picduino_2550_v2.2_0 (saved by Fritzing 0.9.0b)
circuit board: 6.858cm x 5.334cm
breadboards: 1

parts:
  Analog_Pins = FreeSensors-ArduinoAnalogPins [form="♀ (female)"]
  Power_Pins = FreeSensors-ArduinoPowerPins [form="♀ (female)"]
  DigiLow_Pins = FreeSensors-ArduinoDigiLowPins [form="♀ (female)"]
  DigiHigh_Pins = FreeSensors-ArduinoDigiHighPins [form="♀ (female)"]
  PIC_18F2550 = FreeSensors-PIC18F2550 [part_number=18F2550]
  18F4550 = FreeSensors-PIC18F4550 [part_number=18F4550]
  D1 = FreeSensors-1N5817 [part_number=1N5817]
  Power_plug = Power plug
  USB_CONN_B = USB connector [package=THT]
  XTAL1 = Crystal [frequency="20 MHz" package=THT]
  RUN = LED - 3mm [color="Green (560nm)" package="3 mm [THT]"]
  RESET = Pushbutton [package="[THT]"]
  R4 = Resistor [tolerance=±5% resistance=470 package=THT]
  C1 = Ceramic Capacitor [capacitance=22pF package="100 mil [THT, multilayer]"]
  C2 = Ceramic Capacitor [capacitance=22pF package="100 mil [THT, multilayer]"]
  Power = LED - 3mm [color="Red (660nm)" package="3 mm [THT]"]
  R5 = Resistor [tolerance=±5% resistance=470 package=THT]
  C4 = Electrolytic Capacitor [capacitance=22µF voltage=16V package="100 mil [THT, electrolytic]"]
  C5 = Ceramic Capacitor [capacitance=100nF package="100 mil [THT, multilayer]"]
  J3 = female pin header, 3 pins [form="♀ (female)"]
  J2 = female pin header, 3 pins [form="♀ (female)"]
  J5V = female pin header, 3 pins [form="♀ (female)"]
  R3 = Resistor [tolerance=±5% resistance=10k package=THT]
  U1 = Voltage Regulator - 5V [part_number=7805 package="TO220 [THT]"]
  C6 = Electrolytic Capacitor [capacitance=1µF voltage=16V package="100 mil [THT, electrolytic]"]
  SJ1 = Solder Jumper [package=sj_2s-no]
  SJ2 = Solder Jumper [package=sj_2s-no]
  C7 = Ceramic Capacitor [capacitance=100nF package="100 mil [THT, multilayer]"]
  C3 = Ceramic Capacitor [capacitance=220nF package="200 mil [THT, multilayer]"]

nets:
  N1: Analog_Pins.connector0, PIC_18F2550.connector1, 18F4550.connector1
  N2: Analog_Pins.connector1, PIC_18F2550.connector2, 18F4550.connector2
  N3: Analog_Pins.connector2, PIC_18F2550.connector3, 18F4550.connector3
  N4: Analog_Pins.connector3, PIC_18F2550.connector4, 18F4550.connector4
  N5: Analog_Pins.connector4, PIC_18F2550.connector6, 18F4550.connector6
  N6: Analog_Pins.connector5, 18F4550.connector7
  VIN: Power_Pins.connector0, D1.connector0, C4.+, U1.input_voltage, C7.1
  GND: Power_Pins.connector1, Power_Pins.connector2, DigiHigh_Pins.connector6, PIC_18F2550.connector7, PIC_18F2550.connector18, 18F4550.connector11, 18F4550.connector30, Power_plug.GND, USB_CONN_B.GND, USB_CONN_B.chassis5, USB_CONN_B.chassis6, RESET.Pin_1, RESET.Pin_2, C1.0, C2.0, R5.Pin_1, C4.-, C5.1, U1.GND, C6.-, C7.0, C3.0
  5V: Power_Pins.connector3, PIC_18F2550.connector19, 18F4550.connector10, 18F4550.connector31, RUN.anode, Power.anode, C5.0, J5V.pin2, R3.Pin_0, C6.+
  Reset: Power_Pins.connector5, PIC_18F2550.connector0, 18F4550.connector0, RESET.Pin_3, RESET.Pin_4, R3.Pin_1
  N7: DigiLow_Pins.connector0, PIC_18F2550.connector17, 18F4550.connector25
  N8: DigiLow_Pins.connector1, PIC_18F2550.connector16, 18F4550.connector24
  N9: DigiLow_Pins.connector2, PIC_18F2550.connector22, 18F4550.connector34
  N10: DigiLow_Pins.connector3, PIC_18F2550.connector23, 18F4550.connector35
  N11: DigiLow_Pins.connector4, PIC_18F2550.connector24, 18F4550.connector36
  N12: DigiLow_Pins.connector5, J3.pin3, SJ1.1
  N13: DigiLow_Pins.connector6, J2.pin3, SJ2.1
  N14: DigiLow_Pins.connector7, PIC_18F2550.connector25, 18F4550.connector37
  N15: DigiHigh_Pins.connector0, PIC_18F2550.connector10, 18F4550.connector14
  N16: DigiHigh_Pins.connector1, J3.pin1
  N17: DigiHigh_Pins.connector2, J2.pin1
  N18: DigiHigh_Pins.connector3, PIC_18F2550.connector26, 18F4550.connector38
  N19: DigiHigh_Pins.connector4, PIC_18F2550.connector27, 18F4550.connector39
  N20: DigiHigh_Pins.connector5, PIC_18F2550.connector5, 18F4550.connector5, R4.Pin_1
  N21: DigiHigh_Pins.connector8, PIC_18F2550.connector20, 18F4550.connector32
  N22: DigiHigh_Pins.connector9, PIC_18F2550.connector21, 18F4550.connector33
  N23: PIC_18F2550.connector8, 18F4550.connector12, XTAL1.pin_0, C2.1
  N24: PIC_18F2550.connector9, 18F4550.connector13, XTAL1.pin_1, C1.1
  N25: PIC_18F2550.connector11, 18F4550.connector15, J3.pin2
  N26: PIC_18F2550.connector12, 18F4550.connector16, J2.pin2
  N27: PIC_18F2550.connector13, 18F4550.connector17, C3.1
  USB D-: PIC_18F2550.connector14, 18F4550.connector22, USB_CONN_B.d-
  USB D+: PIC_18F2550.connector15, 18F4550.connector23, USB_CONN_B.d+
  N28: 18F4550.connector27, SJ1.2
  N29: 18F4550.connector28, SJ2.2
  N30: D1.connector1, Power_plug.VCC
  N31: USB_CONN_B.5V, J5V.pin1
  N32: RUN.cathode, R4.Pin_0
  N33: Power.cathode, R5.Pin_0
  N34: J5V.pin3, U1.output_voltage

notes:
  FreeSensors
  PICduino
  v2
  USB  Vin
