# Fritzing sketch id2956_PicLabMini_0 (saved by Fritzing 0.9.2b)
circuit board: 8.46667cm x 5.64444cm
breadboards: 1

parts:
  IC1 = PICAXE-40X [part_number=PIC18F4550 package=THT]
  R1 = Resistor [tolerance=±5% resistance=3.3k package=THT]
  C1 = Ceramic Capacitor [capacitance=100nF package="100 mil [THT, multilayer]"]
  C2 = Ceramic Capacitor [capacitance=100nF package="100 mil [THT, multilayer]"]
  C3 = Ceramic Capacitor [capacitance=100nF package="100 mil [THT, multilayer]"]
  C4 = Ceramic Capacitor [capacitance=100nF package="100 mil [THT, multilayer]"]
  XTAL1 = Crystal [frequency="20 MHz" package=THT]
  CONN1 = USB connector [package=THT]
  C5 = Ceramic Capacitor [capacitance=100nF package="100 mil [THT, multilayer]"]
  S1 = Pushbutton [package="[THT]"]
  R2 = Resistor [tolerance=±5% resistance=1k package=THT]
  LED1 = LED - 3mm [color="Red (633nm)" package="3 mm [THT]"]

nets:
  N1: IC1.Reset, R1.Pin_1
  N2: IC1.+V, R1.Pin_0, C1.1, C2.0, CONN1.5V, S1.Pin_1, S1.Pin_2, LED1.anode
  N3: IC1.0V, C1.0, C2.1, C3.1, C4.0, CONN1.GND, CONN1.chassis5, CONN1.chassis6, C5.0, S1.Pin_3, S1.Pin_4, R2.Pin_1
  N4: IC1.Resonator#12, C4.1, XTAL1.pin_1
  N5: IC1.Resonator#13, C3.0, XTAL1.pin_0
  N6: IC1.In/Out_C3, C5.1
  N7: IC1.In/Out_C4, CONN1.d-
  N8: IC1.In/Out_C5, CONN1.d+
  N9: R2.Pin_0, LED1.cathode

notes:
  PicLabMini
