# Fritzing sketch id2957_PID_0 (saved by Fritzing 0.9.3b)
circuit board: 8.46667cm x 5.64444cm
breadboards: 1

parts:
  Componente1 = Arduino Mega 2560 (Rev3)
  R1 = Rotary Potentiometer (Small) [maximum_resistance=100kΩ package=THT]
  C1 = Electrolytic Capacitor [capacitance=1mF voltage=20V package="100 mil [THT, electrolytic]"]
  R2 = Resistor [tolerance=±5% resistance=100 package=THT]

nets:
  N1: Componente1.A0, Componente1.GND, R1.leg2, C1.-, C1.+, R2.Pin_0
  N2: Componente1.D3_PWM, R1.leg1
  N3: R1.wiper, R2.Pin_1
