# Fritzing sketch id2958_PID_V2_0 (saved by Fritzing 0.9.3b)
circuit board: 10cm x 6cm
breadboards: 1

parts:
  Componente2 = Arduino Mega 2560 (Rev3)
  R3 = Rotary Potentiometer (Small) [maximum_resistance=100kΩ package=THT]
  C2 = Electrolytic Capacitor [capacitance=1mF voltage=20V package="100 mil [THT, electrolytic]"]
  R4 = Resistor [tolerance=±5% resistance=100 package=THT]

nets:
  N1: Componente2.A0, C2.+, R4.Pin_0
  N2: Componente2.GND, R3.leg2, C2.-
  N3: Componente2.D3_PWM, R3.leg1
  N4: R3.wiper, R4.Pin_1
