# Fritzing sketch id295_Proyecto_Tarea_01_0 (saved by Fritzing 0.9.3b)
breadboards: 1

parts:
  Componente1 = Arduino Uno (Rev3)
  R1 = Resistor [tolerance=±5% resistance=220 package=THT]
  R2 = Resistor [tolerance=±5% resistance=220 package=THT]
  LED1 = LED - 5mm [color="Red (633nm)" package="5 mm [THT]"]
  LED2 = LED - 5mm [color="Red (633nm)" package="5 mm [THT]"]
  J1 = Piezo Speaker
  Parte3 = HC-SR04 ultrasonic distance sensor
  LED3 = LED - 5mm [color="Red (633nm)" package="5 mm [THT]"]
  R3 = Resistor [tolerance=±5% resistance=220 package=THT]

nets:
  N1: Componente1.D8, J1.pin2
  N2: Componente1.D10_PWM/SS, Parte3.connector2
  N3: Componente1.D11_PWM/MOSI, Parte3.connector1
  N4: Componente1.D3_PWM, LED3.anode
  N5: Componente1.D4, LED2.anode
  N6: Componente1.D5_PWM, LED1.anode
  N7: Componente1.5V, Parte3.connector0
  N8: Componente1.GND, R1.Pin_1, R2.Pin_0, J1.pin1, Parte3.connector3
  N9: R2.Pin_1, LED2.cathode
  N10: LED3.cathode, R3.Pin_1
