# Fritzing sketch id2960_mic_fritzing_design1_0 (saved by Fritzing 0.9.3b)
circuit board: 6.24083cm x 3.03082cm
breadboards: 1

parts:
  Piezo = MIC [package=mic_electret_smd]
  D1 = Diode [package=diode-1n4148]
  D3 = Diode [package=diode-1n4148]
  TL071CP = OP37 - Low Noise, Precision, High Speed Op Amp [part_number=TL071CP]
  R5 = Resistor [tolerance=±10% resistance=150k package=THT]
  R6 = Resistor [tolerance=±5% resistance=33k package=THT]
  R7 = Resistor [tolerance=±5% resistance=1k package=THT]
  3_3M = 3.3MΩ
  C1 = Electrolytic Capacitor [capacitance=1µF package="100 mil [THT, electrolytic]"]
  R9 = Resistor [tolerance=±5% resistance=100k package=THT]
  OUT = female pin header, 2 pins [form="♀ (female)"]
  Vcc = female pin header, 2 pins [form="♀ (female)"]
  4_7M = 4.7 MΩ
  D2 = Diode [package=diode-1n4148]
  Parça1 = Arduino Mega 2560 (Rev3)
  VCC1 = 4 x AAA Battery Mount
  piezo = female pin header, 2 pins [form="♀ (female)"]

nets:
  GND: Piezo.1, TL071CP.-V, R6.Pin_0, 3_3M.connector0, C1.-, R9.Pin_0, OUT.pin2, Vcc.pin1, D2.A, Parça1.GND, VCC1.-, piezo.pin2
  N1: Piezo.2, D1.A, TL071CP.+IN, 3_3M.connector1, D2.C, piezo.pin1
  5V: D1.C, TL071CP.V+, R5.Pin_1, Vcc.pin2, Parça1.VIN, VCC1.+
  N2: D3.A, R7.Pin_1
  N3: D3.C, C1.+, R9.Pin_1, OUT.pin1, Parça1.A0
  N4: TL071CP.-IN, R5.Pin_0, R6.Pin_1, 4_7M.connector0
  N5: TL071CP.OUT, R7.Pin_0, 4_7M.connector1
