# Fritzing sketch id2960_pikachu_I (saved by Fritzing 0.3.8b)

parts:
  U1 = atmega168 [package="DIP28 [THT]"]
  U2 = Voltage Regulator - 5V [package="TO220 [THT]"]
  R1 = basic-resistor_10k_bf174900-d90f-1000-8590-5dba6c7be407
  U3-Resonator = mystery-part_3_a7a36c78-d90f-1000-8589-5dba6c7be407
  R2 = basic-resistor_22k_259cb1c6-d90f-1000-856d-5dba6c7be407
  R2_2 = basic-resistor_22k_259cb1c6-d90f-1000-856d-5dba6c7be407
  R2_3 = basic-resistor_22k_259cb1c6-d90f-1000-856d-5dba6c7be407
  R2_4 = basic-resistor_22k_259cb1c6-d90f-1000-856d-5dba6c7be407
  R1_2 = basic-resistor_10k_bf174900-d90f-1000-8590-5dba6c7be407
  R1_3 = basic-resistor_10k_bf174900-d90f-1000-8590-5dba6c7be407
  R1_4 = basic-resistor_10k_bf174900-d90f-1000-8590-5dba6c7be407
  J1-_reed_switch_connector = generic-female-header_2_643fe902-d90f-1000-857b-5dba6c7be407
  J2_-_LED_connector = generic-female-header_3_72756c54-d90f-1000-8582-5dba6c7be407
  J3-MC_Connector = generic-female-header_5_71f85f4a-7a32-11de-a8cb-0bce54aeec03
  C1 = Electrolytic Capacitor [package=THT]
  C2 = Electrolytic Capacitor [package=THT]
  R3 = basic-resistor_10k_bf174900-d90f-1000-8590-5dba6c7be407
  R4 = basic-resistor_10k_bf174900-d90f-1000-8590-5dba6c7be407
  R5 = basic-resistor_470_7f65bdce-d90f-1000-8597-5dba6c7be407
  C3 = Ceramic Capacitor [package=THT]
  J1 = generic-female-header_2_643fe902-d90f-1000-857b-5dba6c7be407
  C4 = Ceramic Capacitor [package=THT]
  D1 = Rectifier Diode [package=THT]

nets:
  N1: U1.Pin_1, R3.connector1
  N2: U1.Pin_2, J1.connector1
  N3: U1.Pin_3, J1.connector0
  N4: U1.Pin_4, R5.connector1, C3.pin_1, D1.anode
  N5: U1.Pin_5, R2_3.connector0
  N6: U1.Pin_7, U1.Pin_20, U2.output_voltage, C2.+, R3.connector0, R4.connector0, C3.pin_0, C4.pin_1
  N7: U1.Pin_8, U1.Pin_22, R1.connector0, U3-Resonator.connector1, R1_2.connector0, R1_3.connector0, R1_4.connector0, C4.pin_0
  N8: U1.Pin_9, U3-Resonator.connector0
  N9: U1.Pin_10, U3-Resonator.connector2
  N10: U1.Pin_23, R2.connector0
  N11: U1.Pin_24, R2_2.connector0
  N12: U1.Pin_25, R1_4.connector1
  N13: U1.Pin_26, J2_-_LED_connector.connector2
  N14: U1.Pin_27, J2_-_LED_connector.connector1
  N15: U1.Pin_28, J2_-_LED_connector.connector0
  N16: U2.input_voltage, R2.connector1, J3-MC_Connector.connector1, C1.+
  N17: U2.GND, J1-_reed_switch_connector.connector1, J3-MC_Connector.connector0, C1.-, C2.-
  N18: R2_2.connector1, J3-MC_Connector.connector2
  N19: R2_3.connector1, J3-MC_Connector.connector3
  N20: R2_4.connector1, J3-MC_Connector.connector4
  N21: J1-_reed_switch_connector.connector0, R4.connector1, R5.connector0, D1.cathode

notes:
  Voltage dividers
  Debounce Circuit
  Pikachu - Onboard Motorcycle Computer
