# Fritzing sketch id2961_piezo+flexie_0 (saved by Fritzing 0.7.10b)
breadboards: 1

parts:
  R1 = Resistor [tolerance=±5% resistance=10k package=THT]
  R2 = Basic Flex Resistor
  J1 = Piezo Speaker
  Arduino1 = Arduino

nets:
  N1: R1.Pin_0, J1.pin1, Arduino1.GND
  N2: R1.Pin_1, R2.pin_1, Arduino1.A0
  N3: R2.Pin_2, Arduino1.+5V
  N4: J1.pin2, Arduino1.D9
