# Fritzing sketch id2963_Arduino_Piezo_Trigger_RGB_LED_0 (saved by Fritzing 0.9.3b)
breadboards: 1

parts:
  Part1 = Arduino Leonardo (Rev3b)
  U1 = Tri-Color LED SMD [package=led-tricolor-smd]
  R1 = Textile Analog Pressure Sensor [part_number=PW073]
  Q5 = Basic FET N-Channel [package="TO220 [THT]"]
  Q6 = Basic FET N-Channel [package="TO220 [THT]"]
  Q7 = Basic FET N-Channel [package="TO220 [THT]"]
  R2 = Resistor [tolerance=±5% resistance=1M package="0805 [SMD]"]
  U2 = POT [package=alps_pot]

nets:
  N1: Part1.5V, U2.E
  N2: Part1.GND, R1.pin_0, Q5.source, Q6.source, Q7.source, R2.Pin_0, U2.A
  N3: Part1.VIN, U1.A
  N4: Part1.A1, U2.S
  N5: Part1.A5, R1.pin_1, R2.Pin_1
  N6: Part1.D9_PWM/A9, Q5.gate
  N7: Part1.D10_PWM/A10, Q6.gate
  N8: Part1.D11_PWM, Q7.gate
  N9: U1.BLU, Q7.drain
  N10: U1.GRN, Q5.drain
  N11: U1.RED, Q6.drain

notes:
  This must be 12V RGB LED Strip. White input is 12V input
  Arduino must be connected to 12V Adapter to work with LED Strip
  These are "IRL540" MOSFET N-Channel Transistors.
  Buy IRL540 Transistor from GRUP ELEKTRONIK - Selanik Pasaji KARAKÖY
  This must be a simple Piezo Preasure Sensor
  This is a 1 Mega OHM Resistor
  You can flash the RGB LED Strip with a colour you want by hitting the pressure sensor. Adjust the preasure sensitivity with the potentiometer which controls the treshold of the pressure sensor. If the pressure is above the treshold the the LED flashes. If not then the LED will be shining RED.
  This setup is a prototype for a LED Percussion. You can set a trigger system for the percussion instrument. Cover the instrument with the LED Strip. Make a show with playing percussion and flash LED when you play a rhythm.
