# Fritzing sketch id2964_Motortreiberstufe_L293D (saved by Fritzing 0.6.2b)
stripboards: 1

parts:
  IC1 = IC, DIP package, 16 pins [chip_label=L293D spacing=300mil]
  J1 = Screw terminal - 2 pins [package=THT]
  J2 = Screw terminal - 2 pins [package=THT]
  J3 = screw terminal, 4 pins
  J4 = screw terminal, 4 pins

nets:
  N1: IC1.pin1, J4.pin2
  N2: IC1.pin3, J4.pin3
  N3: IC1.pin4, IC1.pin5, J4.pin1
  N4: IC1.pin6, J4.pin4
  N5: IC1.pin8, J1.pin2
  N6: IC1.pin9, J3.pin3
  N7: IC1.pin11, J3.pin1
  N8: IC1.pin12, IC1.pin13, J1.pin1, J2.pin2, J3.pin4
  N9: IC1.pin14, J3.pin2
  N10: IC1.pin16, J2.pin1

notes:
  Vs = 5v
  Vss = 5v -36v
  GND
  Enable2
  Output 4
  Output 3
  GND
  Enable1
  Output 1
  Output 2
