# Fritzing sketch id2965_nke69___arduino___raspberry_0 (saved by Fritzing 0.9.3b)
breadboards: 1

parts:
  arduino_uno_rev3 = Arduino Uno (Rev3)
  LCD_16X2_standard = LCD screen
  R1 = Trimmer Potentiometer [maximum_resistance=10kΩ package=THT]
  R2 = Resistor [tolerance=±5% resistance=220 package=THT]
  Water_Level = LED - 5mm [color="Blue (430nm)" package="5 mm [THT]"]
  R5_* = Resistor [tolerance=±5% resistance=220 package=THT]
  TO_pH-PROBE = BNC [package=bnc]
  pH_Circuit(DFRobot_com) = phboard [part_number="Analog pH Meter Pro SKU:SEN0169"]
  R6 = Resistor [tolerance=±5% resistance=220 package=THT]
  pH_High = LED - 5mm [color="Yellow (592nm)" package="5 mm [THT]"]
  R7 = Resistor [tolerance=±5% resistance=10k package=THT]
  R8 = Resistor [tolerance=±5% resistance=4.7k package=THT]
  C1 = Ceramic Capacitor [capacitance=0.22mF package="0805 [SMD, multilayer]"]
  DS10 = DS18B20_Probe_Cable
  220AC1 = Lilypad Battery Connect
  220AC2 = Lilypad Battery Connect
  220AC3 = Lilypad Battery Connect
  220AC4 = Lilypad Battery Connect
  Raspberry_Pi_4 = Raspberry Pi 3 [part_number=RPI-3-V1.2]
  M1 = DC Motor [part_number="Pompe Niveau eau"]
  M2 = DC Motor [part_number="2 * Pompe de brassage"]
  M3 = DC Motor [part_number="Lampe meuble"]
  M4 = DC Motor [part_number="Pompe à air"]
  RPICam_to_Pi_with_CSI_Cable1 = TRANSCHIPTC5747 [package=camera_sfv24r-2st_2]  # not connected
  Relais_1 = 4ChannelRelay
  R5_*1 = Resistor [tolerance=±5% resistance=220 package=THT]
  Heat_Low = LED - 5mm [color="Green (565nm)" package="5 mm [THT]"]
  S1 = SWITCH-MOMENTARY-2 [package=reed_switch_plastic]
  Relais_2 = 4ChannelRelay
  Capteur_de_porte = LilyPad Light Sensor
  Temp_Min = POT [package=3362u]
  Temp_Max = POT [package=3362u]
  Set_pH_Value = POT [package=3362u]
  R3_* = Resistor [tolerance=±5% resistance=220 package=THT]
  Heat_High = LED - 5mm [color="Red (633nm)" package="5 mm [THT]"]
  R10 = Resistor [tolerance=±5% resistance=470 package=THT]
  DHT2 = DHT22_Humidity_and_Temperature_Sensor
  part = Electrolytic Capacitor [capacitance=10μF voltage=50V package="0605 [SMD, electrolytic]"]

nets:
  N1: arduino_uno_rev3.A1, Temp_Min.S
  N2: arduino_uno_rev3.A2, Temp_Max.S
  N3: arduino_uno_rev3.A3, pH_Circuit(DFRobot_com).connector2
  N4: arduino_uno_rev3.A4/SDA, Set_pH_Value.S
  N5: arduino_uno_rev3.A5/SCL, R5_*1.Pin_1, Heat_Low.anode
  N6: arduino_uno_rev3.D8, Water_Level.anode, R6.Pin_0
  N7: arduino_uno_rev3.D9_PWM, R8.Pin_1, DS10.connector2
  N8: arduino_uno_rev3.D10_PWM/SS, R5_*.Pin_1, pH_High.anode
  N9: arduino_uno_rev3.D11_PWM/MOSI, LCD_16X2_standard.E
  N10: arduino_uno_rev3.D12/MISO, LCD_16X2_standard.RS
  N11: arduino_uno_rev3.D13/SCK, R10.Pin_1, DHT2.connector2
  N12: arduino_uno_rev3.D2, LCD_16X2_standard.DB7
  N13: arduino_uno_rev3.D3_PWM, LCD_16X2_standard.DB6
  N14: arduino_uno_rev3.D4, LCD_16X2_standard.DB5
  N15: arduino_uno_rev3.D5_PWM, LCD_16X2_standard.DB4
  N16: arduino_uno_rev3.D6_PWM, R3_*.Pin_1, Heat_High.anode
  N17: arduino_uno_rev3.D7, R7.Pin_1, S1.1
  N18: arduino_uno_rev3.RESET, part.+
  5V: arduino_uno_rev3.5V, LCD_16X2_standard.VDD, LCD_16X2_standard.LED+, R1.leg1, pH_Circuit(DFRobot_com).connector1, R8.Pin_0, C1.1, DS10.connector3, S1.2, Temp_Min.E, Temp_Max.E, Set_pH_Value.E, R10.Pin_0, DHT2.connector1
  GND: arduino_uno_rev3.GND, LCD_16X2_standard.VSS, LCD_16X2_standard.R/W, R1.leg2, R2.Pin_1, Water_Level.cathode, R5_*.Pin_0, pH_Circuit(DFRobot_com).connector0, R6.Pin_1, pH_High.cathode, R7.Pin_0, C1.0, DS10.connector1, R5_*1.Pin_0, Heat_Low.cathode, Temp_Min.A, Temp_Max.A, Set_pH_Value.A, R3_*.Pin_0, Heat_High.cathode, DHT2.connector4, part.-
  N19: LCD_16X2_standard.V0, R1.wiper
  N20: LCD_16X2_standard.LED-, R2.Pin_0
  N21: TO_pH-PROBE.GND, pH_Circuit(DFRobot_com).connector5
  N22: TO_pH-PROBE.OUT, pH_Circuit(DFRobot_com).connector4
  N23: 220AC1.-, Relais_1.connector13
  N24: 220AC1.+, M2.pin_2
  N25: 220AC2.-, Relais_1.connector16
  N26: 220AC2.+, M1.pin_2
  N27: 220AC3.-, Relais_1.connector9
  N28: 220AC3.+, M3.pin_2
  N29: 220AC4.-, Relais_1.connector6
  N30: 220AC4.+, M4.pin_2
  N31: Raspberry_Pi_4.GND, Relais_1.connector1, Relais_2.connector1, Capteur_de_porte.-
  N32: Raspberry_Pi_4.GPIO17, Relais_1.connector3
  N33: Raspberry_Pi_4.GPIO27, Capteur_de_porte.+
  N34: Raspberry_Pi_4.GPIO5, Relais_2.connector2
  N35: Raspberry_Pi_4.GPIO6, Relais_2.connector3
  N36: Raspberry_Pi_4.GPIO13, Relais_2.connector17
  N37: Raspberry_Pi_4.GPIO19, Relais_2.connector10
  N38: Raspberry_Pi_4.GPIO21, Relais_1.connector10
  N39: Raspberry_Pi_4.GPIO20, Relais_1.connector17
  N40: Raspberry_Pi_4.GPIO18, Relais_1.connector2
  N41: Raspberry_Pi_4.5V, Relais_1.connector0, Relais_2.connector0
  N42: M1.pin_1, Relais_1.connector15
  N43: M2.pin_1, Relais_1.connector12
  N44: M3.pin_1, Relais_1.connector8
  N45: M4.pin_1, Relais_1.connector5

notes:
  Capteur de Niveau Read
  0 ou 1
  condensateur 22nf afin de ne pas avoir d'interférence avec l'écran LCD lorsque les relais active ou désactive le 220V
  Relais 1
  ------------------------------
  PIN4 : 5VCC ROUGE
  PIN6 : GROUND NOIR
  PIN11 GPIO18 VERT IN1
  PIN12 GPIO17 BLEU IN2
  PIN38 GPIO 20 ORANGE IN3
  PIN40 GPIO21 GRIS IN4
  Relais 2
  ------------------------------
  PIN2 : 5VCC ROUGE
  PIN14 : GROUND NOIR
  PIN29 GPIO5 VERT IN1
  PIN31 GPIO6 BLEU IN2
  PIN33 GPIO13 ORANGE IN3
  PIN35 GPIO19 GRIS IN4
  PIN13 GPIO27 BLANC
  PIN9 GND NOIR
  capacitor 10uF pour desactiver le reset du port Com de l'arduino
