# Fritzing sketch id2966_Pigeonier1_0 (saved by Fritzing 0.8.5b)
breadboards: 1

parts:
  Composants1 = Arduino Nano (Rev3.0)
  LED1 = LED - 5mm [color="Red (633nm)" package="5 mm [THT]"]
  R1 = Resistor [tolerance=±5% resistance=220 package=THT]
  SPKR1 = Loudspeaker  # not connected
  Q1 = NPN-Transistor [package="TO92 [THT]"]
  R2 = Resistor [tolerance=±5% resistance=10k package=THT]
  J1 = Basic Servo  # not connected

nets:
  N1: Composants1.GND, LED1.anode, Q1.E
  N2: Composants1.5V, R1.Pin_0, R2.Pin_1
  N3: Composants1.A0, Q1.C, R2.Pin_0
  N4: LED1.cathode, R1.Pin_1
