# Fritzing sketch id2967_Pikey_0 (saved by Fritzing 0.9.2b)
breadboards: 1

parts:
  Teensy_3_1 = Teensy 3.0
  Raspberry_Pi1 = Raspberry Pi 2
  VCC1 = Battery

nets:
  GND: Teensy_3_1.GND, Raspberry_Pi1.GND
  N1: Teensy_3_1.D0, Raspberry_Pi1.GPIO14
  N2: Teensy_3_1.D1, Raspberry_Pi1.GPIO15
  N3: Teensy_3_1.D11, Raspberry_Pi1.GPIO9
  N4: Teensy_3_1.D12, Raspberry_Pi1.GPIO10
  N5: Teensy_3_1.VBat, VCC1.-
  N6: Teensy_3_1.D13, Raspberry_Pi1.GPIO11
  N7: Teensy_3_1.AGND, VCC1.+
  VIN: Teensy_3_1.Vin, Raspberry_Pi1.5V
  N8: Teensy_3_1.D29, Raspberry_Pi1.GPIO3
  N9: Teensy_3_1.D30, Raspberry_Pi1.GPIO2
