# Fritzing sketch id2968_Moteur_Pas_a_Pas_0 (saved by Fritzing 0.9.3b)

parts:
  Composant1 = Arduino Uno (Rev3)
  NEMA17 = Stepper Motor - Bipolar
  S1 = Ponte-H L298N
  Alim_12v = 2.1mm_Barrel_Jack_with_Terminal_Block
  Reglage_Vitesse = Rotary Potentiometer (Large) [maximum_resistance=100kΩ package=THT]
  1_Pas = Momentary Switch [package=ksa_sealed_tac_switch]
  Sens_de_marche = Momentary Switch [package=ksa_sealed_tac_switch]
  On_/_Off = Momentary Switch [package=ksa_sealed_tac_switch]
  Sens_Marche = smd LED [color="Green (555nm)" package="0603 [SMD]"]
  On_/_Off_2 = smd LED [color="Red (633nm)" package="0603 [SMD]"]
  R2 = Resistor [tolerance=±5% resistance=220 package=THT]
  R3 = Resistor [tolerance=±5% resistance=220 package="0603 [SMD]"]
  R4 = Resistor [tolerance=±5% resistance=10k package=THT]
  R5 = Resistor [tolerance=±5% resistance=10k package=THT]
  R6 = Resistor [tolerance=±5% resistance=10k package=THT]
  Common_Stepper = X113647
  28BYJ-48 = Adafruit_Gear_reduced_Stepper_Motor
  Alim_12v_2 = 2.1mm_Barrel_Jack_with_Terminal_Block

nets:
  N1: Composant1.A0, Reglage_Vitesse.wiper
  N2: Composant1.D8, S1.connector5
  N3: Composant1.D9_PWM, S1.connector6
  N4: Composant1.D10_PWM/SS, S1.connector7
  N5: Composant1.D11_PWM/MOSI, S1.connector8
  N6: Composant1.D3_PWM, 1_Pas.3
  N7: Composant1.D4, Sens_Marche.anode
  N8: Composant1.D5_PWM, Sens_de_marche.2
  N9: Composant1.D6_PWM, On_/_Off_2.anode
  N10: Composant1.D7, On_/_Off.2
  N11: Composant1.5V, Reglage_Vitesse.leg2
  N12: Composant1.GND, Reglage_Vitesse.leg1
  N13: NEMA17.A, S1.connector10
  N14: NEMA17.C, S1.connector11
  N15: NEMA17.B, S1.connector14
  N16: NEMA17.D, S1.connector13
  N17: S1.connector1, Alim_12v.connector1
  N18: S1.connector2, Alim_12v.connector2
  N19: 1_Pas.1, R4.Pin_1
  N20: Sens_de_marche.1, On_/_Off.1
  N21: Sens_de_marche.4, R5.Pin_1
  N22: On_/_Off.4, R6.Pin_1
  N23: Sens_Marche.cathode, R2.Pin_1
  N24: On_/_Off_2.cathode, R3.Pin_1
  N25: R2.Pin_0, R3.Pin_0
  N26: Common_Stepper.connector5, Alim_12v_2.connector2
  N27: Common_Stepper.connector6, Alim_12v_2.connector1
  N28: Common_Stepper.connector7, 28BYJ-48.connector5
  N29: Common_Stepper.connector8, 28BYJ-48.connector4
  N30: Common_Stepper.connector9, 28BYJ-48.connector3
  N31: Common_Stepper.connector10, 28BYJ-48.connector2
  N32: Common_Stepper.connector11, 28BYJ-48.connector1

notes:
  Vers GND de l'Arduino
  Stepper MonMoteur(NbrPas,8, 10, 9, 11) pour 28BYJ-48
  Stepper MonMoteur(NbrPas,8, 9, 10, 11) pour NEMA17
