# Fritzing sketch id296_Arduino_Alexa_0 (saved by Fritzing 0.9.3b)
breadboards: 1

parts:
  SP1 = SPEAKER [package=pcb_mount_speaker]
  Part2 = Breakout Board for Electret Microphone
  Part1 = Arduino Uno (Rev3)
  LED1 = LED - 5mm [color="Green (555nm)" package="5 mm [THT]"]
  R1 = Resistor [tolerance=±5% resistance=220 package=THT]

nets:
  GND: SP1.+, Part2.GND, Part1.GND, LED1.cathode
  N1: SP1.-, Part1.D3_PWM
  N2: Part2.VCC, Part1.A0
  N3: Part2.AUD, Part1.3V3
  N4: Part1.D6_PWM, R1.Pin_1
  N5: LED1.anode, R1.Pin_0
