# Fritzing sketch id2972_ping_pongv2_0 (saved by Fritzing 0.9.0b)
breadboards: 1

parts:
  Raspberry_Pi1 = Raspberry_Pi_B+
  R2 = Resistor [tolerance=±5% resistance=1k package=THT]
  R9 = Resistor [tolerance=±5% resistance=1k package=THT]
  R12 = Resistor [tolerance=±5% resistance=1k package=THT]
  R14 = Resistor [tolerance=±5% resistance=1k package=THT]
  R16 = Resistor [tolerance=±5% resistance=1k package=THT]
  R17 = Resistor [tolerance=±5% resistance=1k package=THT]
  R18 = Resistor [tolerance=±5% resistance=1k package=THT]
  R19 = Resistor [tolerance=±5% resistance=1k package=THT]
  R20 = Resistor [tolerance=±5% resistance=1k package=THT]
  R21 = Resistor [tolerance=±5% resistance=1k package=THT]
  R22 = Resistor [tolerance=±5% resistance=220 package=THT]
  S1 = Pushbutton [package="[THT]"]
  S2 = Pushbutton [package="[THT]"]
  4511 = IC, DIP package, 16 pins [chip_label=4511]  # not connected
  4511_2 = IC, DIP package, 16 pins [chip_label=4511]
  U1 = 7-SEGMENT-DISPLAY-1_-RED [package=7-segment-1_pth]
  U2 = 7-SEGMENT-DISPLAY-1_-RED [package=7-segment-1_pth]
  LED1 = LED - 5mm [color="Red (633nm)" package="5 mm [THT]"]
  LED2 = LED - 5mm [color="Red (633nm)" package="5 mm [THT]"]
  LED3 = LED - 5mm [color="Red (633nm)" package="5 mm [THT]"]
  LED4 = LED - 5mm [color="Red (633nm)" package="5 mm [THT]"]
  LED5 = LED - 5mm [color="Red (633nm)" package="5 mm [THT]"]
  LED6 = LED - 5mm [color="Red (633nm)" package="5 mm [THT]"]
  U3 = Buzzer [chip_label=Buzzer]

nets:
  N1: Raspberry_Pi1.connector0, S1.Pin_3, S1.Pin_4, S2.Pin_1, S2.Pin_2, 4511_2.pin3, 4511_2.pin4, 4511_2.pin16
  N2: Raspberry_Pi1.connector3, R2.Pin_1
  N3: Raspberry_Pi1.connector14, R20.Pin_1
  N4: Raspberry_Pi1.connector15, R21.Pin_1
  N5: Raspberry_Pi1.connector16, U3.connector1
  N6: Raspberry_Pi1.connector17, 4511_2.pin7
  N7: Raspberry_Pi1.connector18, 4511_2.pin2
  N8: Raspberry_Pi1.connector20, R9.Pin_1
  N9: Raspberry_Pi1.connector21, 4511_2.pin6
  N10: Raspberry_Pi1.connector22, 4511_2.pin1
  N11: Raspberry_Pi1.connector29, R19.Pin_1
  N12: Raspberry_Pi1.connector31, R18.Pin_1
  N13: Raspberry_Pi1.connector32, R17.Pin_1
  N14: Raspberry_Pi1.connector37, R12.Pin_1, R14.Pin_1, R22.Pin_1, 4511_2.pin5, 4511_2.pin8, LED1.cathode, LED2.cathode, LED3.cathode, LED4.cathode, LED5.cathode, LED6.cathode
  N15: R2.Pin_0, S1.Pin_1, S1.Pin_2
  N16: R9.Pin_0, S2.Pin_3, S2.Pin_4
  N17: R12.Pin_0, U2.G2
  N18: R14.Pin_0, U1.G2
  N19: R16.Pin_0, LED1.anode
  N20: R17.Pin_0, LED2.anode
  N21: R18.Pin_0, LED3.anode
  N22: R19.Pin_0, LED4.anode
  N23: R20.Pin_0, LED5.anode
  N24: R21.Pin_0, LED6.anode
  N25: R22.Pin_0, U3.connector0
  N26: 4511_2.pin9, U1.E
  N27: 4511_2.pin10, U1.D
  N28: 4511_2.pin11, U1.C
  N29: 4511_2.pin12, U1.B
  N30: 4511_2.pin13, U1.A
  N31: 4511_2.pin14, U1.G
  N32: 4511_2.pin15, U1.F
