# Fritzing sketch id2974_ping_pong_0 (saved by Fritzing 0.9.2b)
breadboards: 1

parts:
  GLCD_128x1 = 128 x 64 Graphic LCD
  Componente1 = Arduino Uno (Rev3)
  U1 = POT [package=pot_alpha_rv16af-20]
  S1 = Momentary Switch [package=ksa_sealed_tac_switch]
  S2 = Momentary Switch [package=ksa_sealed_tac_switch]
  R1 = Resistor [tolerance=±5% resistance=10k package="0805 [SMD]"]
  R2 = Resistor [tolerance=±5% resistance=10k package="0805 [SMD]"]

nets:
  N1: GLCD_128x1.1_Vss, GLCD_128x1.15_CS1, Componente1.GND, U1.A, R1.Pin_0, R2.Pin_0
  N2: GLCD_128x1.2_Vdd, GLCD_128x1.19_A(+), Componente1.5V, U1.E, S1.3, S2.3
  N3: GLCD_128x1.4_D/I, Componente1.D11_PWM/MOSI
  N4: GLCD_128x1.5_R/W, Componente1.D12/MISO
  N5: GLCD_128x1.6_Enable, Componente1.D13/SCK
  N6: GLCD_128x1.20_K(-), U1.S
  N7: Componente1.D8, S2.1, R2.Pin_1
  N8: Componente1.D9_PWM, S1.1, R1.Pin_1

notes:
  mov left
  mov right
  Ping pong game by Alessandro Oss©
  Player:0 Arduino:1
  ] °
  [
