# Fritzing sketch id2975_circuito_PipiFun_0 (saved by Fritzing 0.7.7b)
breadboards: 1

parts:
  IC1 = L293D [package=THT]
  S1 = Pushbutton [package="[THT]"]
  S2 = Pushbutton [package="[THT]"]
  S3 = Pushbutton [package="[THT]"]
  S4 = Pushbutton [package=THT]
  S5 = Pushbutton [package=THT]
  S6 = Pushbutton [package=THT]
  R1 = Resistor [tolerance=±5% resistance=1k package=THT]
  R2 = Resistor [tolerance=±5% resistance=1k package=THT]
  R3 = Resistor [tolerance=±5% resistance=1k package=THT]
  R4 = Resistor [tolerance=±5% resistance=1k package=THT]
  R5 = Resistor [tolerance=±5% resistance=1k package=THT]
  R6 = Resistor [tolerance=±5% resistance=1k package=THT]
  Arduino1 = Arduino
  C3 = Ceramic Capacitor [package=THT]
  C4 = Ceramic Capacitor [package=THT]
  R7 = Resistor [tolerance=±5% resistance=1k package=THT]
  LED1 = LED - 5mm [color="Yellow (585nm)" package="5 mm [THT]"]
  M1 = DC Motor
  M2 = DC Motor

nets:
  N1: IC1.Enable_1, Arduino1.D4
  N2: IC1.In_1, Arduino1.D3
  N3: IC1.Out_1_(_Controlled_by_Enable_1_), M1.pin_2
  N4: IC1.0V, R1.Pin_1, R2.Pin_1, R3.Pin_1, R4.Pin_1, R5.Pin_1, R6.Pin_1, Arduino1.GND, C3.pin_0, C4.pin_0, LED1.cathode
  N5: IC1.Out_2_(_Controlled_by_Enable_1_), M1.pin_1
  N6: IC1.In_2, Arduino1.D9
  N7: IC1.+Vmotor, S4.leg1, S5.leg1, S6.leg1, C3.pin_1
  N8: IC1.Enable_2, Arduino1.D7
  N9: IC1.In_3, Arduino1.D6
  N10: IC1.Out_3_(_Controlled_by_Enable_2_), M2.pin_2
  N11: IC1.Out_4_(_Controlled_by_Enable_2_), M2.pin_1
  N12: IC1.In_4, Arduino1.D5
  N13: IC1.+V, S1.Pin_3, S1.Pin_4, S2.Pin_3, S2.Pin_4, S3.Pin_3, S3.Pin_4, Arduino1.+5V, C4.pin_1
  N14: S1.Pin_1, S1.Pin_2, R1.Pin_0, Arduino1.D1TX
  N15: S2.Pin_1, S2.Pin_2, R2.Pin_0, Arduino1.D12
  N16: S3.Pin_1, S3.Pin_2, R3.Pin_0, Arduino1.D11
  N17: S4.leg0, R4.Pin_0, Arduino1.D13
  N18: S5.leg0, R5.Pin_0, Arduino1.D8
  N19: S6.leg0, R6.Pin_0, Arduino1.D2
  N20: Arduino1.D10, R7.Pin_1
  N21: R7.Pin_0, LED1.anode
