# Fritzing sketch id2978_Pir_sensor_and_photo_sensor_mix_0 (saved by Fritzing 0.9.3b)
breadboards: 1

parts:
  Part1 = Arduino Uno (Rev3)
  LED1 = LED - 5mm [color="Green (565nm)" package="5 mm [THT]"]
  R1 = Resistor [tolerance=±2% resistance=100 package=THT]
  U1 = TMP36 [package=to-92]
  J1 = Piezo Speaker
  R2 = PHOTOCELL [package=photocell-kit]
  R3 = Resistor [tolerance=±5% resistance=330 package="0402 [SMD]"]

nets:
  N1: Part1.A0, R2.P$1, R3.Pin_1
  N2: Part1.D10_PWM/SS, LED1.anode, J1.pin2
  N3: Part1.D2, U1.VOUT
  N4: Part1.3V3, R3.Pin_0
  5V: Part1.5V, R1.Pin_1, U1.VCC
  GND: Part1.GND, U1.GND, R2.P$2
  N5: LED1.cathode, R1.Pin_0, J1.pin1
