# Fritzing sketch id2979_Pir_sensor_and_photo_sensor_mix_Y5lmYl2_0 (saved by Fritzing 0.9.3b)
breadboards: 1

parts:
  Part1 = Arduino Uno (Rev3)
  LED1 = LED - 5mm [color="Green (565nm)" package="5 mm [THT]"]
  R1 = Resistor [tolerance=±2% resistance=100 package=THT]
  J1 = Piezo Speaker
  R2 = PHOTOCELL [package=photocell-kit]
  R3 = Resistor [tolerance=±5% resistance=330 package="0402 [SMD]"]
  PIR1 = pir

nets:
  N1: Part1.A0, R2.P$1, R3.Pin_1
  N2: Part1.D10_PWM/SS, LED1.anode, J1.pin2
  N3: Part1.D2, PIR1.connector2
  N4: Part1.3V3, R3.Pin_0
  N5: Part1.5V, R1.Pin_1, PIR1.connector1
  N6: Part1.GND, R2.P$2, PIR1.connector3
  N7: LED1.cathode, R1.Pin_0, J1.pin1
