# Fritzing sketch id297_Arduino_Aliseo_4_Relle_0 (saved by Fritzing 0.7.0b)
breadboards: 1

parts:
  Arduino1 = Arduino [part_number="Aliseo V 0.1"]
  Ventil4 = RJ45
  DS1820 = PNP-Transistor [part_number="Sensore DS18B20" package="TO92 [THT]"]
  R1 = Resistor [tolerance=±5% resistance=10k package=THT]
  Ventil1 = RJ45
  Ventil3 = RJ45
  Ventil2 = RJ45

nets:
  N1: Arduino1.GND, Ventil4.connector4, DS1820.E, Ventil1.connector4, Ventil3.connector4, Ventil2.connector4
  N2: Arduino1.D8, Arduino1.D4, Ventil1.connector2
  N3: Arduino1.D7, Ventil3.connector2
  N4: Arduino1.D6, Ventil2.connector2
  N5: Arduino1.D5, Ventil4.connector2
  N6: Arduino1.D2, Ventil4.connector5, DS1820.B, R1.Pin_1, Ventil1.connector5, Ventil3.connector5, Ventil2.connector5
  N7: Arduino1.+5V, Ventil4.connector6, DS1820.C, R1.Pin_0, Ventil1.connector6, Ventil3.connector6, Ventil2.connector6
