# Fritzing sketch id2980_pir_fritzing_0 (saved by Fritzing 0.8.7b)
breadboards: 1

parts:
  Part1 = Arduino Uno (Rev3)
  LED1 = LED - 5mm [color="Red (633nm)" package="5 mm [THT]"]
  R1 = Resistor [tolerance=±5% resistance=220 package=THT]
  PIR1 = PIR_sensor

nets:
  N1: Part1.D13/SCK, R1.Pin_0
  N2: Part1.D7, PIR1.connector2
  N3: Part1.5V, PIR1.connector1
  N4: Part1.GND, LED1.cathode, PIR1.connector3
  N5: LED1.anode, R1.Pin_1
