# Fritzing sketch id2981_Relais_und_PIR_0 (saved by Fritzing 0.9.3b)
breadboards: 1

parts:
  Raspberry_Pi_1 = Raspberry Pi 3 [part_number=RPI-3-V1.2]
  K1 = Relay [part_number=FRS1B-S package=THT]
  LED1 = Super Flux LED blue [color=Blue]

nets:
  N1: Raspberry_Pi_1.5V, K1.C1, K1.C2, LED1.anode
