# Fritzing sketch id2982_pir_sensor_0 (saved by Fritzing 0.9.2b)
breadboards: 1

parts:
  PIR1 = PIR_sensor
  Composant1 = Arduino Uno (Rev3)

nets:
  N1: PIR1.connector1, Composant1.5V
  N2: PIR1.connector2, Composant1.D2
  N3: PIR1.connector3, Composant1.GND
