# Fritzing sketch id2983_Piscar_um_Led_0 (saved by Fritzing 0.9.3b)
breadboards: 1

parts:
  LED1 = LED - 5mm [color="Red (633nm)" package="5 mm [THT]"]
  Componente1 = Arduino Uno (Rev3)
  R1 = Resistor [tolerance=±20% resistance=330 package=THT]

nets:
  N1: LED1.cathode, Componente1.GND
  N2: LED1.anode, R1.Pin_0
  N3: Componente1.D10_PWM/SS, R1.Pin_1
