# Fritzing sketch id2985_Piscine_0 (saved by Fritzing 0.7.12b)

parts:
  Arduino1 = Arduino
  LCD1 = LCD screen
  K1 = Relay [part_number=FRS1B-S package=THT]  # not connected
  T1 = LM35 Temperature Sensor [package="TO92 [THT]"]  # not connected
  T2 = LM35 Temperature Sensor [package="TO92 [THT]"]  # not connected
  R1 = Resistor [tolerance=±5% resistance=220 package=THT]  # not connected

nets:
  N1: Arduino1.D7, LCD1.DB7
  N2: Arduino1.D6, LCD1.DB6
  N3: Arduino1.D5, LCD1.DB5
  N4: Arduino1.D4, LCD1.DB4
  N5: Arduino1.D3, LCD1.E
  N6: Arduino1.D2, LCD1.RS
  +5V: Arduino1.+5V, LCD1.VDD
  N7: Arduino1.GND, LCD1.DB3
