# Fritzing sketch id2986_pistaduino_fritzing_0 (saved by Fritzing 0.9.3b)
breadboards: 1

parts:
  Componente1 = Arduino Uno (Rev3)
  hc-sr1 = hc-sr04

nets:
  N1: Componente1.D4, hc-sr1.Echo
  N2: Componente1.D5_PWM, hc-sr1.Trig
  5V: Componente1.5V, hc-sr1.VCC
  GND: Componente1.GND, hc-sr1.GND
