# Fritzing sketch id2987_schema_computer_attiny_rev2_0 (saved by Fritzing 0.8.5b)
circuit board: 5.947cm x 4.14292cm

parts:
  U1 = attiny85 [package=dip]
  R1 = Resistor [tolerance=±5% resistance=220 package=THT]
  LED1 = LED - 5mm [color="Blue (430nm)" package="5 mm [THT]"]
  J1 = female pin header, 8 pins [form="♀ (female)"]
  J2 = female pin header, 4 pins [form="♀ (female)"]
  J3 = female pin header, 2 pins [form="♀ (female)"]
  J4 = female pin header, 2 pins [form="♀ (female)"]
  J6 = female pin header, 1 pin [form="♀ (female)"]
  J7 = female pin header, 1 pin [form="♀ (female)"]

nets:
  N1: U1.Pin_1, J2.pin1
  N2: U1.Pin_2, J1.pin5
  N3: U1.Pin_3, J1.pin4
  N4: U1.Pin_4, R1.Pin_1, J1.pin1, J1.pin2, J3.pin2
  N5: U1.Pin_5, LED1.anode, J1.pin8, J2.pin2, J6.pin1, J7.pin1
  N6: U1.Pin_6, J1.pin7, J2.pin3
  N7: U1.Pin_7, J1.pin6, J2.pin4
  N8: U1.Pin_8, J1.pin3, J3.pin1
  N9: R1.Pin_0, J4.pin2
  N10: LED1.cathode, J4.pin1

notes:
  PitDuino rev2 - 11/2014
  GND
  5V
  ~0
  ~1
  2-A0
  3-A1
  4-A2
  SCK
  www.zappoco.altervista.org
  MISO
  MOSI
  RESET
  R1
  PWRL
  2
  1
  0
  attiny
