# Fritzing sketch id2988_PitFdTduino_V07b_0 (saved by Fritzing 0.9.1b)
circuit board: 8.32988cm x 5.83609cm
breadboards: 1

parts:
  ATmega_328 = atmega328 [package=dip]
  16MHz = Crystal [frequency="16 Mhz" package=THT]
  10kΩ = Resistor [tolerance=±5% resistance=1k package=THT]
  220Ω = Resistor [tolerance=±5% resistance=220 package=THT]
  LED13 = LED - 5mm [color="Red (633nm)" package="5 mm [THT]"]
  10uF = Capacitor Polarized [part_number=C2 package=cpol-radial-10uf-25v]
  10uF_2 = Capacitor Polarized [part_number=C1 package=cpol-radial-10uf-25v]
  POWER = Power plug
  L7805 = Voltage Regulator - 5V [package="TO220 [THT]"]
  J4 = female pin header, 4 pins [form="♀ (female)"]
  Componente1 = Arduino Uno (Rev3)  # not connected
  D7-D0 = female pin header, 8 pins [form="♀ (female)"]
  D13-D9 = female pin header, 6 pins [form="♀ (female)"]
  PWR = female pin header, 2 pins [form="♀ (female)"]
  J7 = male pin header, 6 pins [form="♂ (male)"]
  J5 = female pin header, 1 pin [form="♀ (female)"]
  A0-A5 = female pin header, 6 pins [form="♀ (female)"]
  PWR_2 = female pin header, 6 pins [form="♀ (female)"]
  P13 = double row male pin header, 2 pins [form="♂ (male)"]
  J10 = female pin header, 1 pin [form="♀ (female)"]
  J8 = female pin header, 1 pin [form="♀ (female)"]
  J11 = female pin header, 1 pin [form="♀ (female)"]
  100_nF = Ceramic Capacitor [capacitance=100nF package="200 mil [THT, multilayer]"]
  RESET = Momentary Switch [package=tactile-pth]
  22pF = Ceramic Capacitor [capacitance=10pF package="200 mil [THT, multilayer]"]
  22pF_2 = Ceramic Capacitor [capacitance=100nF package="200 mil [THT, multilayer]"]

nets:
  N1: ATmega_328.RESET, 10kΩ.Pin_0, J7.pin1, PWR_2.pin1, 100_nF.0, RESET.3
  N2: ATmega_328.D0_(RX), J4.pin2, D7-D0.pin1
  N3: ATmega_328.D1_(TX), J4.pin1, D7-D0.pin2
  N4: ATmega_328.D2, D7-D0.pin3
  N5: ATmega_328.D3_(PWM), D7-D0.pin4
  N6: ATmega_328.D4, D7-D0.pin5
  N7: ATmega_328.VCC, ATmega_328.AVCC, ATmega_328.AREF, 10kΩ.Pin_1, 10uF.+, L7805.output_voltage, J4.pin4, PWR.pin1, J7.pin6, PWR_2.pin3
  GND: ATmega_328.GND, LED13.anode, 10uF.-, 10uF_2.-, POWER.GND, L7805.GND, J4.pin3, PWR.pin2, J7.pin5, PWR_2.pin4, PWR_2.pin5, J10.pin1, J11.pin1, RESET.1, 22pF.0, 22pF_2.1
  N8: ATmega_328.XLAT1, 16MHz.pin_0, 22pF.1
  N9: ATmega_328.XLAT2, 16MHz.pin_1, 22pF_2.0
  N10: ATmega_328.D5_(PWM), D7-D0.pin6
  N11: ATmega_328.D6_(PWM), D7-D0.pin7
  N12: ATmega_328.D7, D7-D0.pin8
  N13: ATmega_328.D8, D13-D9.pin6
  N14: ATmega_328.D9_(PWM), D13-D9.pin5
  N15: ATmega_328.D10_(PWM), D13-D9.pin4
  N16: ATmega_328.D11_(PWM), D13-D9.pin3, J7.pin3
  N17: ATmega_328.D12, D13-D9.pin2, J7.pin2
  N18: ATmega_328.D13, 220Ω.Pin_0, D13-D9.pin1, J7.pin4
  N19: ATmega_328.A0, A0-A5.pin6
  N20: ATmega_328.A1, A0-A5.pin5
  N21: ATmega_328.A2, A0-A5.pin4
  N22: ATmega_328.A3, A0-A5.pin3
  N23: ATmega_328.A4, A0-A5.pin2
  N24: ATmega_328.A5, A0-A5.pin1
  N25: 220Ω.Pin_1, P13.pin1
  N26: LED13.cathode, P13.pin2
  N27: 10uF_2.+, POWER.VCC, L7805.input_voltage, J8.pin1
  N28: J5.pin1, 100_nF.1

notes:
  PitFtdDuino - V07b
  GND
  5V
  RXD<0
  13
  PitBTHC05
  RXD
  TXD
  TX0>1
  2
  ~3
  DTR
  12
  ~11
  ~10
  ~9
  4
  ~6
  ~5
  7
  8
  A0
  A1
  A2
  A3
  A4
  A5
  MOSI
  MISO
  SCK
  RST
  USB - ASP
  www.zappoco.altervista.org
  02/2015
