# Fritzing sketch id2989_A_PitIR_receiverV02_0 (saved by Fritzing 0.9.1b)
circuit board: 2.39925cm x 1.49614cm
breadboards: 1

parts:
  C1 = Electrolytic Capacitor [capacitance=4.7µF package="100 mil [THT, electrolytic]"]
  R1 = Resistor [tolerance=±5% resistance=100 package=THT]
  J1 = female pin header, 3 pins [form="♀ (female)"]
  J2 = female pin header, 3 pins [form="♀ (female)"]

nets:
  N1: C1.-, J1.pin2, J2.pin3
  N2: C1.+, R1.Pin_0, J1.pin3
  N3: R1.Pin_1, J2.pin2
  N4: J1.pin1, J2.pin1

notes:
  PitIR 2.0
  V - S
  - V S
  by zappoco
