# Fritzing sketch id2990_A_PitMotorV08_arduino_mini_0 (saved by Fritzing 0.9.1b)
circuit board: 8.81637cm x 4.73134cm

parts:
  Componente1 = Arduino Pro Mini v13  # not connected
  IC4 = L293D [package=THT]
  J18 = female pin header, 12 pins [form="♀ (female)"]
  J15 = female pin header, 12 pins [form="♀ (female)"]
  J17 = female pin header, 12 pins [form="♀ (female)"]
  J16 = female pin header, 8 pins [form="♀ (female)"]
  J19 = male pin header, 4 pins [form="♂ (male)"]
  J21 = male pin header, 3 pins [form="♂ (male)"]
  J20 = male pin header, 3 pins [form="♂ (male)"]
  J12 = screw terminal, 2 pins
  J13 = screw terminal, 2 pins
  J14 = screw terminal, 2 pins

nets:
  N1: IC4.Enable_1, J21.pin2
  N2: IC4.In_1, J17.pin2
  N3: IC4.Out_1_(_Controlled_by_Enable_1_), J14.pin2
  N4: IC4.0V, J18.pin11, J15.pin2, J17.pin9, J16.pin5, J13.pin2
  N5: IC4.Out_2_(_Controlled_by_Enable_1_), J14.pin1
  N6: IC4.In_2, J17.pin1
  N7: IC4.+Vmotor, J13.pin1
  N8: IC4.Enable_2, J20.pin2
  N9: IC4.In_3, J17.pin3
  N10: IC4.Out_3_(_Controlled_by_Enable_2_), J12.pin2
  N11: IC4.Out_4_(_Controlled_by_Enable_2_), J12.pin1
  N12: IC4.In_4, J17.pin4
  N13: IC4.+V, J18.pin9, J15.pin4, J21.pin1, J20.pin1
  N14: J18.pin1, J15.pin12
  N15: J18.pin2, J15.pin11, J19.pin4
  N16: J18.pin3, J15.pin10, J19.pin3
  N17: J18.pin4, J15.pin9, J19.pin2
  N18: J18.pin5, J15.pin8
  N19: J18.pin6, J15.pin7
  N20: J18.pin7, J15.pin6
  N21: J18.pin8, J15.pin5
  N22: J18.pin10, J15.pin3, J19.pin1
  N23: J18.pin12, J15.pin1
  N24: J17.pin5, J16.pin1
  N25: J17.pin6, J16.pin2, J20.pin3
  N26: J17.pin7, J16.pin3
  N27: J17.pin8, J16.pin4, J21.pin3
  N28: J17.pin10, J16.pin6
  N29: J17.pin11, J16.pin7
  N30: J17.pin12, J16.pin8

notes:
  PitMotor rev8 - 01/2015
  GND
  M2
  M1
  3V
  12
  A0
  A1
  A2
  A3
  VCC
  ~5
  ~3
  RST
  RX1
  TX0
  RAW
  13
  11
  10
  MOSI
  MISO
  SCK
  UsbAsp
  EN
  4
  PitMotor rev4 - 12/2014
  2
  ~4A
  3A
  1A
  ~2A
  www.zappoco.altervista.org
  Arduino Pro Mini
