# Fritzing sketch id2991_PixelPals_0 (saved by Fritzing 0.9.3b)
breadboards: 1

parts:
  Raspberry_Pi_Zero1 = Raspberry Pi Zero
  Q1 = NPN-Transistor [package="TO92 [THT]"]
  LED1 = LED - 5mm [color="Red (633nm)" package="5 mm [THT]"]
  R1 = Resistor [tolerance=±5% resistance=330k package=THT]

nets:
  N1: Raspberry_Pi_Zero1.3v3, LED1.cathode
  N2: Raspberry_Pi_Zero1.GPIO2, R1.Pin_0
  N3: Raspberry_Pi_Zero1.GND, Q1.C
  N4: Q1.E, LED1.anode
  N5: Q1.B, R1.Pin_1
