# Fritzing sketch id2994_PJON_uno_esp8266_with_logic_level_converter_0 (saved by Fritzing 0.9.2b)
breadboards: 1

parts:
  Part1 = Logic Level Converter
  Part2 = Arduino Uno (Rev3)
  U1 = NodeMCU
  R1 = Resistor [tolerance=±5% resistance=1.5k package="0603 [SMD]"]
  R2 = Resistor [tolerance=±5% resistance=10k package="0603 [SMD]"]

nets:
  GND: Part1.GND, Part2.GND, U1.connector13
  N1: Part1.LV, U1.connector14
  N2: Part1.TX_LV, U1.connector1, R1.Pin_0
  N3: Part1.TX_HV, Part2.D12/MISO, R2.Pin_1
  N4: Part1.HV, Part2.5V

notes:
  Every board gets its own power, feeding it into the logic level converter
  10K pull-down resistor
  5v
  3.3v
  1.5K pull-down resistor
