# Fritzing sketch id2995_PKE___1___13_0 (saved by Fritzing 0.9.1b)
circuit board: 2cm x 3cm
breadboards: 1

parts:
  VCC1 = Battery block 9V
  R1 = Resistor [tolerance=±5% resistance=470 package=THT]
  R2 = Resistor [tolerance=±5% resistance=1k package=THT]
  LED1 = LED - 5mm [color="Red (633nm)" package="5 mm [THT]"]
  R3 = Photocell (LDR) [package=THT]  # not connected
  J1 = female pin header, 2 pins [form="♀ (female)"]

nets:
  N1: VCC1.-, R2.Pin_1
  N2: VCC1.+, LED1.anode
  N3: R1.Pin_0, J1.pin2
  N4: R1.Pin_1, R2.Pin_0
  N5: LED1.cathode, J1.pin1
