# Fritzing sketch id2997_PKE___1___16_0 (saved by Fritzing 0.9.1b)
breadboards: 1

parts:
  LED1 = RGB LED - (4 legs) [package="5 mm [THT]"]
  VCC1 = Battery block 9V
  R1 = Resistor [tolerance=±5% resistance=470 package=THT]
  R2 = Resistor [tolerance=±5% resistance=10k package=THT]
  R4 = Resistor [tolerance=±5% resistance=10k package=THT]
  R3 = Resistor [tolerance=±5% resistance=33k package=THT]
  R5 = Resistor [tolerance=±5% resistance=10k package=THT]
  R7 = Resistor [tolerance=±5% resistance=10k package=THT]
  R6 = Resistor [tolerance=±5% resistance=10k package=THT]

nets:
  N1: LED1.red_cathode, R2.Pin_0, R5.Pin_0
  N2: LED1.common_anode, R1.Pin_1
  N3: LED1.green_cathode, R3.Pin_0
  N4: LED1.blue_cathode, R4.Pin_0, R7.Pin_0, R6.Pin_0
  N5: VCC1.-, R2.Pin_1, R4.Pin_1, R3.Pin_1, R5.Pin_1, R7.Pin_1, R6.Pin_1
  N6: VCC1.+, R1.Pin_0
