# Fritzing sketch id2998_PKE___1___17_0 (saved by Fritzing 0.9.1b)
breadboards: 1

parts:
  VCC1 = Battery block 9V
  J1 = female pin header, 2 pins [form="♀ (female)"]
  LED1 = LED - 5mm [color="Green (555nm)" package="5 mm [THT]"]
  J2 = Piezo Speaker

nets:
  N1: VCC1.-, J2.pin1
  N2: VCC1.+, J1.pin1
  N3: J1.pin2, LED1.anode
  N4: LED1.cathode, J2.pin2
