# Fritzing sketch id2999_PKE___1___19_0 (saved by Fritzing 0.9.1b)
breadboards: 1

parts:
  U1 = Transformer [package=transformer]
  R1 = Resistor [tolerance=±5% resistance=2.2k package=THT]
  LED2 = LED - 5mm [color="Blue (430nm)" package="5 mm [THT]"]
  LED1 = LED - 5mm [color="Red (633nm)" package="5 mm [THT]"]
  D1 = Rectifier Diode [part_number=1N4148 package="300 mil [THT]"]
  D3 = Rectifier Diode [part_number=1N4148 package="300 mil [THT]"]
  D4 = Rectifier Diode [part_number=1N4148 package="300 mil [THT]"]
  D2 = Rectifier Diode [part_number=1N4148 package="300 mil [THT]"]
  C1 = Electrolytic Capacitor [capacitance=100µF package="100 mil [THT, electrolytic]"]
  J1 = Piezo Speaker

nets:
  N1: U1.3, LED2.anode, LED1.cathode, D3.cathode, D4.anode
  N2: U1.4, R1.Pin_0, D1.cathode, D2.anode
  N3: R1.Pin_1, LED2.cathode, LED1.anode
  N4: D1.anode, D3.anode, C1.-, J1.pin1
  N5: D4.cathode, D2.cathode, C1.+, J1.pin2
