# Fritzing sketch id2999_multipleBlink (saved by Fritzing 0.9.3b)
breadboards: 1

parts:
  Part1 = Arduino Uno (Rev3)
  LED1 = LED - 5mm [color="Blue (525nm)" package="5 mm [THT]"]
  LED2 = LED - 5mm [color="Blue (525nm)" package="5 mm [THT]"]
  LED3 = LED - 5mm [color="Blue (525nm)" package="5 mm [THT]"]
  R1 = Resistor [tolerance=±5% resistance=220 package=THT]
  R2 = Resistor [tolerance=±5% resistance=220 package=THT]
  R3 = Resistor [tolerance=±5% resistance=220 package=THT]

nets:
  N1: Part1.D13/SCK, LED1.anode, LED2.anode, LED3.anode
  N2: Part1.GND, R1.Pin_1, R2.Pin_1, R3.Pin_1
  N3: LED1.cathode, R1.Pin_0
  N4: LED2.cathode, R2.Pin_0
  N5: LED3.cathode, R3.Pin_0
