# Fritzing sketch id299_Schematic_0 (saved by Fritzing 0.9.3b)
circuit board: 8.46667cm x 5.64444cm
breadboards: 1

parts:
  Part1 = Arduino Uno (Rev3)
  R1 = Rotary Potentiometer (Large) [maximum_resistance=100kΩ package=THT]
  R2 = Photocell (LDR) [package=THT]
  LED1 = RGB LED (com. cathode, rgb) [package="5 mm [THT]"]
  R3 = Resistor [tolerance=±5% resistance=330 package=THT]
  R4 = Resistor [tolerance=±5% resistance=330 package=THT]
  R5 = Resistor [tolerance=±5% resistance=330 package=THT]
  R6 = Resistor [tolerance=±5% resistance=10k package=THT]
  S1 = Pushbutton [package="[THT]"]
  R7 = Resistor [tolerance=±5% resistance=10k package=THT]

nets:
  N1: Part1.A0, R2.pin_0, R6.Pin_1
  N2: Part1.A1, R1.wiper
  N3: Part1.D9_PWM, R5.Pin_0
  N4: Part1.D10_PWM/SS, R4.Pin_0
  N5: Part1.D11_PWM/MOSI, R3.Pin_0
  N6: Part1.D12/MISO, S1.Pin_1, S1.Pin_2, R7.Pin_1
  N7: Part1.5V, R1.leg1, R2.pin_1, R7.Pin_0
  N8: Part1.GND, R1.leg2, LED1.green_anode, R6.Pin_0, S1.Pin_3, S1.Pin_4
  N9: LED1.red_anode, R3.Pin_1
  N10: LED1.common_cathode, R4.Pin_1
  N11: LED1.blue_anode, R5.Pin_1
