# Fritzing sketch id29_sram_1024k_0 (saved by Fritzing 0.9.0b)
circuit board: 1.65871cm x 3.3751cm
breadboards: 1

parts:
  IC1 = 25LC512 [package=THT]
  IC2 = 25LC512 [package=THT]
  R1 = Resistor [tolerance=±5% resistance=220 package=THT]
  R2 = Resistor [tolerance=±5% resistance=220 package=THT]
  J1 = male pin header, 6 pins [form="♂ (male)"]

nets:
  CS: IC1.CS_-_Chip_Select, IC2.CS_-_Chip_Select, J1.pin1
  N1: IC1.SO_-_Data_Out, IC2.SI_-_Data_In
  N2: IC1.WP_-_Write_Protect, IC1.0V, R1.Pin_0
  MOSI/SI: IC1.SI_-_Data_In, J1.pin2
  SCK: IC1.SCK_-_SPI_Clock, IC2.SCK_-_SPI_Clock, J1.pin4
  +V/V+: IC1.+V, IC2.+V, J1.pin5
  MISO/SO: IC2.SO_-_Data_Out, J1.pin3
  N3: IC2.WP_-_Write_Protect, IC2.0V, R2.Pin_0
  GND: R1.Pin_1, R2.Pin_1, J1.pin6
