# Fritzing sketch id3000_PKE___1___21_0 (saved by Fritzing 0.9.1b)
breadboards: 1

parts:
  VCC1 = Battery block 9V
  LED1 = LED - 5mm [color="Red (633nm)" package="5 mm [THT]"]
  R1 = Resistor [tolerance=±5% resistance=1k package=THT]
  S1 = Pushbutton [package=THT]
  S2 = Pushbutton [package=THT]
  C1 = Electrolytic Capacitor [capacitance=10µF package="100 mil [THT, electrolytic]"]
  R2 = Resistor [tolerance=±5% resistance=1k package=THT]
  LED2 = LED - 5mm [color="Yellow (585nm)" package="5 mm [THT]"]
  J1 = Piezo Speaker

nets:
  N1: VCC1.-, C1.-, LED2.cathode, J1.pin1
  N2: VCC1.+, LED1.anode
  N3: LED1.cathode, R1.Pin_0
  N4: R1.Pin_1, S1.leg1
  N5: S1.leg0, S2.leg1, C1.+
  N6: S2.leg0, R2.Pin_0
  N7: R2.Pin_1, LED2.anode, J1.pin2
