# Fritzing sketch id3001_PKE___1___Projekt_0 (saved by Fritzing 0.9.1b)
breadboards: 1

parts:
  VCC1 = Battery block 9V
  LED1 = LED - 5mm [color="Green (555nm)" package="5 mm [THT]"]
  R1 = Resistor [tolerance=±5% resistance=1k package=THT]
  LED2 = LED - 5mm [color="Red (633nm)" package="5 mm [THT]"]
  R2 = Resistor [tolerance=±5% resistance=1k package=THT]
  D1 = Rectifier Diode [part_number=1N4001 package="300 mil [THT]"]
  C1 = Electrolytic Capacitor [capacitance=0.1mF package="100 mil [THT, electrolytic]"]
  J1 = Piezo Speaker

nets:
  N1: VCC1.-, R1.Pin_1, R2.Pin_1, C1.-, J1.pin1
  N2: LED1.cathode, R1.Pin_0
  N3: LED2.cathode, R2.Pin_0
  N4: LED2.anode, D1.anode
  N5: D1.cathode, C1.+, J1.pin2
