# Fritzing sketch id3002_PKE___2___3a_0 (saved by Fritzing 0.9.1b)
breadboards: 1

parts:
  VCC1 = Battery block 9V
  R1 = Resistor [tolerance=±5% resistance=1k package=THT]
  Q1 = NPN-Transistor [package="TO92 [THT]"]
  RX = Resistor [tolerance=±5% resistance=10M package=THT]
  LED1 = LED - 5mm [color="Blue (430nm)" package="5 mm [THT]"]
  LED2 = LED - 5mm [color="Blue (430nm)" package="5 mm [THT]"]
  R2 = Resistor [tolerance=±5% resistance=1k package=THT]

nets:
  N1: VCC1.-, Q1.E
  N2: VCC1.+, R1.Pin_0, R2.Pin_0
  N3: R1.Pin_1, RX.Pin_0
  N4: Q1.B, LED1.cathode
  N5: Q1.C, LED2.cathode
  N6: RX.Pin_1, LED1.anode
  N7: LED2.anode, R2.Pin_1
