# Fritzing sketch id3003_PKE___2___3b_0 (saved by Fritzing 0.9.1b)
breadboards: 1

parts:
  VCC1 = Battery block 9V
  Q1 = PNP-Transistor [package="TO92 [THT]"]
  LED1 = LED - 5mm [color="Blue (430nm)" package="5 mm [THT]"]
  RX = Resistor [tolerance=±5% resistance=10M package=THT]
  R1 = Resistor [tolerance=±5% resistance=1k package=THT]
  LED2 = LED - 5mm [color="Blue (430nm)" package="5 mm [THT]"]
  R2 = Resistor [tolerance=±5% resistance=1k package=THT]

nets:
  N1: VCC1.-, R1.Pin_1, R2.Pin_1
  N2: VCC1.+, Q1.E
  N3: Q1.B, LED1.anode
  N4: Q1.C, LED2.anode
  N5: LED1.cathode, RX.Pin_0
  N6: RX.Pin_1, R1.Pin_0
  N7: LED2.cathode, R2.Pin_0
