# Fritzing sketch id3005_PKE___2___5a_0 (saved by Fritzing 0.9.1b)
circuit board: 10.3736cm x 6.18594cm
breadboards: 1

parts:
  T2 = PNP-Transistor [package="TO92 [THT]"]
  T1 = PNP-Transistor [package="TO92 [THT]"]
  T3 = NPN-Transistor [package="TO92 [THT]"]
  R15* = Resistor [tolerance=±5% resistance=100k package=THT]
  LED1 = LED - 5mm [color="Red (633nm)" package="5 mm [THT]"]
  D1 = Rectifier Diode [part_number=1N4001 package="300 mil [THT]"]
  R15 = Resistor [tolerance=±5% resistance=4.7k package=THT]
  R14 = Resistor [tolerance=±5% resistance=22k package=THT]
  R12 = Resistor [tolerance=±5% resistance=1M package=THT]
  R13 = Resistor [tolerance=±5% resistance=1M package=THT]
  X = female pin header, 1 pin [form="♀ (female)"]
  J1 = male pin header, 1 pin [form="♂ (male)"]
  J2 = male pin header, 1 pin [form="♂ (male)"]
  Pad1 = Pad [width=3 height=3 connect=center]  # not connected
  Pad2 = Pad [width=3 height=3 connect=center]  # not connected
  R1 = Resistor [tolerance=±5% resistance=2.2k package=THT]
  R2 = Resistor [tolerance=±5% resistance=2.2k package=THT]
  R3 = Resistor [tolerance=±5% resistance=2.2k package=THT]
  R4 = Resistor [tolerance=±5% resistance=2.2k package=THT]
  R5 = Resistor [tolerance=±5% resistance=1k package=THT]
  R6 = Resistor [tolerance=±5% resistance=1k package=THT]
  R7 = Resistor [tolerance=±5% resistance=47k package=THT]
  R8 = Resistor [tolerance=±5% resistance=47k package=THT]
  R9 = Resistor [tolerance=±5% resistance=2.2k package=THT]
  FR = Photocell (LDR) [package=THT]
  RX = Resistor [tolerance=±5% resistance=10k package=THT]
  RY = Resistor [tolerance=±5% resistance=10k package=THT]
  S1 = Pushbutton [package=THT]
  R10 = Resistor [tolerance=±5% resistance=4.7k package=THT]
  R11 = Resistor [tolerance=±5% resistance=4.7k package=THT]
  S2 = Pushbutton [package=THT]
  C1 = Electrolytic Capacitor [capacitance=1mF package="200 mil [THT, electrolytic]"]
  VCC1 = Battery block 9V
  E = female pin header, 1 pin [form="♀ (female)"]
  D = female pin header, 1 pin [form="♀ (female)"]
  C = female pin header, 1 pin [form="♀ (female)"]
  B = female pin header, 1 pin [form="♀ (female)"]
  A = female pin header, 1 pin [form="♀ (female)"]
  F1 = female pin header, 1 pin [form="♀ (female)"]
  F2 = female pin header, 1 pin [form="♀ (female)"]
  G = female pin header, 1 pin [form="♀ (female)"]
  H = female pin header, 1 pin [form="♀ (female)"]
  J = female pin header, 1 pin [form="♀ (female)"]

nets:
  N1: T2.E, T3.B, R14.Pin_1
  N2: T2.B, T1.E
  N3: T2.C, T1.C, R15.Pin_1, R13.Pin_1, J2.pin1, R4.Pin_1, R6.Pin_1, R8.Pin_1, FR.pin_1, RY.Pin_1, R11.Pin_1, C1.-, VCC1.-, A.pin1
  N4: T1.B, R12.Pin_1, R13.Pin_0
  N5: T3.E, D1.anode
  N6: T3.C, R15*.Pin_1, LED1.cathode
  N7: R15*.Pin_0, LED1.anode, R14.Pin_0, J1.pin1, R1.Pin_0, R5.Pin_0, R7.Pin_0, R9.Pin_0, RX.Pin_0, S1.leg1, VCC1.+, E.pin1
  N8: D1.cathode, R15.Pin_0
  N9: R12.Pin_0, X.pin1, R10.Pin_1, S2.leg0, C1.+, J.pin1
  N10: R1.Pin_1, R2.Pin_0, D.pin1
  N11: R2.Pin_1, R3.Pin_0, C.pin1
  N12: R3.Pin_1, R4.Pin_0, B.pin1
  N13: R5.Pin_1, R6.Pin_0, F1.pin1
  N14: R7.Pin_1, R8.Pin_0, F2.pin1
  N15: R9.Pin_1, FR.pin_0, G.pin1
  N16: RX.Pin_1, RY.Pin_0, H.pin1
  N17: S1.leg0, R10.Pin_0
  N18: R11.Pin_0, S2.leg1
