# Fritzing sketch id3006_PKE___2___8_0 (saved by Fritzing 0.9.1b)
circuit board: 10.3736cm x 6.18594cm
breadboards: 1
perfboards: 1

parts:
  T3 = PNP-Transistor [package="TO92 [THT]"]
  T2 = PNP-Transistor [package="TO92 [THT]"]
  T4 = NPN-Transistor [package="TO92 [THT]"]
  R7* = Resistor [tolerance=±5% resistance=100k package=THT]
  LED3 = LED - 5mm [color="Red (633nm)" package="5 mm [THT]"]
  D1 = Rectifier Diode [part_number=1N4001 package="300 mil [THT]"]
  R6 = Resistor [tolerance=±5% resistance=4.7k package=THT]
  R5 = Resistor [tolerance=±5% resistance=22k package=THT]
  R3 = Resistor [tolerance=±5% resistance=470k package=THT]
  R4 = Resistor [tolerance=±5% resistance=470k package=THT]
  Y = female pin header, 1 pin [form="♀ (female)"]
  J4 = male pin header, 1 pin [form="♂ (male)"]
  J2 = male pin header, 1 pin [form="♂ (male)"]
  VCC1 = Battery block 9V
  T5 = PNP-Transistor [package="TO92 [THT]"]
  T6 = PNP-Transistor [package="TO92 [THT]"]
  T7 = NPN-Transistor [package="TO92 [THT]"]
  R9 = Resistor [tolerance=±5% resistance=22k package=THT]
  R11* = Resistor [tolerance=±5% resistance=100k package=THT]
  LED4 = LED - 5mm [color="Red (633nm)" package="5 mm [THT]"]
  D2 = Rectifier Diode [part_number=1N4001 package="300 mil [THT]"]
  R10 = Resistor [tolerance=±5% resistance=4.7k package=THT]
  R8 = Resistor [tolerance=±5% resistance=1M package=THT]
  R8_2 = Resistor [tolerance=±5% resistance=1M package=THT]
  X = female pin header, 1 pin [form="♀ (female)"]
  J2_2 = male pin header, 1 pin [form="♂ (male)"]
  J1 = male pin header, 1 pin [form="♂ (male)"]
  T1 = NPN-Transistor [package="TO92 [THT]"]
  R1 = Resistor [tolerance=±5% resistance=10M package=THT]
  B = female pin header, 1 pin [form="♀ (female)"]
  A = female pin header, 1 pin [form="♀ (female)"]
  LED1 = LED - 5mm [color="Yellow (595nm)" package="5 mm [THT]"]
  R2 = Resistor [tolerance=±5% resistance=1k package=THT]
  LED2 = LED - 5mm [color="Yellow (595nm)" package="5 mm [THT]"]
  R11 = Resistor [tolerance=±5% resistance=1M package=THT]
  A_2 = female pin header, 1 pin [form="♀ (female)"]
  B_2 = female pin header, 1 pin [form="♀ (female)"]

nets:
  N1: T3.E, T4.B, R5.Pin_1
  N2: T3.B, T2.E
  N3: T3.C, T2.C, R6.Pin_1, R4.Pin_1, J2.pin1, VCC1.-, T5.C, T6.C, R10.Pin_1, R8.Pin_1, J2_2.pin1, T1.E
  N4: T2.B, R3.Pin_1, R4.Pin_0
  N5: T4.E, D1.anode
  N6: T4.C, R7*.Pin_1, LED3.cathode
  N7: R7*.Pin_0, LED3.anode, R5.Pin_0, J4.pin1, VCC1.+, R9.Pin_0, R11*.Pin_0, LED4.anode, J1.pin1, LED1.anode, LED2.anode
  N8: D1.cathode, R6.Pin_0
  N9: R3.Pin_0, Y.pin1, T1.C, R2.Pin_1
  N10: T5.E, T6.B
  N11: T5.B, R8.Pin_0, R8_2.Pin_1
  N12: T6.E, T7.B, R9.Pin_1
  N13: T7.E, D2.anode
  N14: T7.C, R11*.Pin_1, LED4.cathode
  N15: D2.cathode, R10.Pin_0
  N16: R8_2.Pin_0, X.pin1, T1.B, R1.Pin_1, B.pin1, R11.Pin_1, B_2.pin1
  N17: R1.Pin_0, A.pin1, LED1.cathode, R11.Pin_0, A_2.pin1
  N18: R2.Pin_0, LED2.cathode
