# Fritzing sketch id3007_PKE___2___Projekt___wersja_prosta_0 (saved by Fritzing 0.9.1b)
breadboards: 1

parts:
  VCC1 = Battery block 9V
  R1 = Resistor [tolerance=±5% resistance=1M package=THT]
  T1 = NPN-Transistor [package="TO92 [THT]"]
  T2 = NPN-Transistor [package="TO92 [THT]"]
  R2 = Resistor [tolerance=±5% resistance=4.7k package=THT]
  C1 = Ceramic Capacitor [capacitance=1µF package="100 mil [THT, multilayer]"]
  J1 = Piezo Speaker

nets:
  N1: VCC1.-, T2.E, C1.0
  N2: VCC1.+, R1.Pin_0, R2.Pin_0, J1.pin2
  N3: R1.Pin_1, T1.B, C1.1
  N4: T1.E, T2.B
  N5: T1.C, R2.Pin_1
  N6: T2.C, J1.pin1
