# Fritzing sketch id3008_PKE___2___Projekt___wersja_wzbogacona_0 (saved by Fritzing 0.9.1b)
breadboards: 1

parts:
  VCC1 = Battery block 9V
  T1 = NPN-Transistor [package="TO92 [THT]"]
  C1 = Ceramic Capacitor [capacitance=100nF package="100 mil [THT, multilayer]"]
  R1 = Resistor [tolerance=±5% resistance=1M package=THT]
  R2 = Resistor [tolerance=±5% resistance=47k package=THT]
  C2 = Ceramic Capacitor [capacitance=100nF package="100 mil [THT, multilayer]"]
  D1 = Rectifier Diode [part_number=1N4001 package="300 mil [THT]"]
  T2 = PNP-Transistor [package="TO92 [THT]"]
  T3 = PNP-Transistor [package="TO92 [THT]"]
  R3 = Resistor [tolerance=±5% resistance=47k package=THT]
  R12 = Resistor [tolerance=±5% resistance=100k package=THT]
  R5 = Resistor [tolerance=±5% resistance=1M package=THT]
  R4 = Resistor [tolerance=±5% resistance=1M package=THT]
  C6 = Ceramic Capacitor [capacitance=100nF package="100 mil [THT, multilayer]"]
  D2 = Rectifier Diode [part_number=1N4001 package="300 mil [THT]"]
  C3 = Ceramic Capacitor [capacitance=1µF package="100 mil [THT, multilayer]"]
  T4 = NPN-Transistor [package="TO92 [THT]"]
  R6 = Resistor [tolerance=±5% resistance=10k package=THT]
  R7 = Resistor [tolerance=±5% resistance=10k package=THT]
  T5 = PNP-Transistor [package="TO92 [THT]"]
  R8 = Resistor [tolerance=±5% resistance=22k package=THT]
  J1 = Piezo Speaker
  LED1 = LED - 5mm [color="Red (633nm)" package="5 mm [THT]"]
  R11 = Resistor [tolerance=±5% resistance=4.7k package=THT]
  T7 = PNP-Transistor [package="TO92 [THT]"]
  C5 = Ceramic Capacitor [capacitance=10nF package="100 mil [THT, multilayer]"]
  R10 = Resistor [tolerance=±5% resistance=10k package=THT]
  T6 = NPN-Transistor [package="TO92 [THT]"]
  R9 = Resistor [tolerance=±5% resistance=10k package=THT]
  C4 = Ceramic Capacitor [capacitance=10nF package="100 mil [THT, multilayer]"]

nets:
  N1: VCC1.-, T1.E, T1.B, C1.0, C1.1, R1.Pin_1, R12.Pin_1, C6.0, T4.E, J1.pin1, T6.E, R9.Pin_1, C4.1
  N2: VCC1.+, R1.Pin_0, R2.Pin_0, D1.cathode, T2.E, T3.E, R4.Pin_0, D2.cathode, R7.Pin_0, T5.E, LED1.anode
  N3: T1.C, R2.Pin_1, C2.1
  N4: C2.0, D1.anode, T2.B
  N5: T2.C, T3.C, R3.Pin_0
  N6: T3.B, R5.Pin_0, R4.Pin_1
  N7: R3.Pin_1, R12.Pin_0, C6.1, T4.B
  N8: R5.Pin_1, D2.anode, C3.0
  N9: C3.1, T4.C, R6.Pin_1
  N10: R6.Pin_0, R7.Pin_1, T5.B
  N11: T5.C, R8.Pin_0, J1.pin2
  N12: R8.Pin_1, T7.C, T6.B, R9.Pin_0, C4.0
  N13: LED1.cathode, R11.Pin_0
  N14: R11.Pin_1, T7.E, C5.1, R10.Pin_0
  N15: T7.B, C5.0, R10.Pin_1, T6.C
