# Fritzing sketch id300_drv8825_arduino_1.2_0 (saved by Fritzing 0.9.3b)
circuit board: 8.46667cm x 5.64444cm
breadboards: 1

parts:
  Power_12V = Power plug  # not connected
  Part1 = Arduino Ethernet Shield (Rev3)
  Pololu_A1 = Pololu A4988 [package=SO16]  # not connected
  Pololu_A2 = Pololu A4988 [package=SO16]  # not connected
  Pololu_A3 = Pololu A4988 [package=SO16]
  MOTOR1 = prefix101206  # not connected
  MOTOR2 = prefix101206  # not connected
  MOTOR3 = prefix101206  # not connected

nets:
  N1: Part1.D2, Pololu_A3.STEP
  N2: Part1.PWM_D5, Pololu_A3.DIR
