# Fritzing sketch id3012_PKE___3___14b_0 (saved by Fritzing 0.9.2b)
breadboards: 1

parts:
  VCC1 = Battery block 9V
  R1 = Resistor [tolerance=±5% resistance=2.2k package=THT]
  R5 = Resistor [tolerance=±5% resistance=10k package=THT]
  LED1 = LED - 5mm [color="Green (555nm)" package="5 mm [THT]"]
  R4 = Resistor [tolerance=±5% resistance=100k package=THT]
  T2 = NPN-Transistor [package="TO92 [THT]"]
  R2 = Resistor [tolerance=±5% resistance=2.2k package=THT]
  LED2 = LED - 5mm [color="Red (635nm)" package="5 mm [THT]"]
  R6 = Resistor [tolerance=±5% resistance=10k package=THT]
  C1 = Electrolytic Capacitor [capacitance=0.1mF package="100 mil [THT, electrolytic]"]
  LED3 = LED - 5mm [color="White (6500K)" package="5 mm [THT]"]
  T1 = PNP-Transistor [package="TO92 [THT]"]
  R3 = Resistor [tolerance=±5% resistance=100k package=THT]
  S1 = Pushbutton [package=THT]
  R7 = Resistor [tolerance=±5% resistance=4.7k package=THT]
  R8 = Resistor [tolerance=±5% resistance=100k package=THT]

nets:
  N1: VCC1.-, R5.Pin_1, LED1.cathode, R4.Pin_1, T2.E, LED3.anode, R7.Pin_1
  N2: VCC1.+, LED2.anode, R6.Pin_0, T1.E, S1.leg1
  N3: R1.Pin_0, C1.+, T1.C
  N4: R1.Pin_1, R5.Pin_0, LED1.anode
  N5: R4.Pin_0, T2.B, R8.Pin_1
  N6: T2.C, R2.Pin_1
  N7: R2.Pin_0, LED2.cathode, R6.Pin_1
  N8: C1.-, LED3.cathode, R8.Pin_0
  N9: T1.B, R3.Pin_1
  N10: R3.Pin_0, S1.leg0, R7.Pin_0
