# Fritzing sketch id3013_PKE___3___15_0 (saved by Fritzing 0.9.2b)
breadboards: 1

parts:
  VCC1 = Battery block 9V
  R3 = Resistor [tolerance=±5% resistance=100k package=THT]
  T1 = NPN-Transistor [package="TO92 [THT]"]
  R7 = Resistor [tolerance=±5% resistance=2.2k package=THT]
  LED1 = LED - 5mm [color="Red (635nm)" package="5 mm [THT]"]
  LED3 = LED - 5mm [color="White (6500K)" package="5 mm [THT]"]
  R4 = Resistor [tolerance=±5% resistance=100k package=THT]
  C1 = Electrolytic Capacitor [capacitance=0.1mF package="100 mil [THT, electrolytic]"]
  S1 = Pushbutton [package=THT]
  R1 = Resistor [tolerance=±5% resistance=2.2k package=THT]
  LED2 = LED - 5mm [color="Red (635nm)" package="5 mm [THT]"]
  LED4 = LED - 5mm [color="White (6500K)" package="5 mm [THT]"]
  R8 = Resistor [tolerance=±5% resistance=2.2k package=THT]
  R5 = Resistor [tolerance=±5% resistance=100k package=THT]
  R6 = Resistor [tolerance=±5% resistance=100k package=THT]
  T2 = NPN-Transistor [package="TO92 [THT]"]
  C2 = Electrolytic Capacitor [capacitance=0.1mF package="100 mil [THT, electrolytic]"]
  S2 = Pushbutton [package=THT]
  R2 = Resistor [tolerance=±5% resistance=2.2k package=THT]

nets:
  N1: VCC1.-, T1.E, LED3.anode, R4.Pin_1, R1.Pin_1, LED4.anode, R6.Pin_1, T2.E, S2.leg1
  N2: VCC1.+, LED1.anode, S1.leg0, LED2.anode, R2.Pin_0
  N3: R3.Pin_0, LED3.cathode, C1.-
  N4: R3.Pin_1, T1.B, R4.Pin_0
  N5: T1.C, R7.Pin_1
  N6: R7.Pin_0, LED1.cathode
  N7: C1.+, S1.leg1, R1.Pin_0
  N8: LED2.cathode, R8.Pin_0
  N9: LED4.cathode, R5.Pin_0, C2.-
  N10: R8.Pin_1, T2.C
  N11: R5.Pin_1, R6.Pin_0, T2.B
  N12: C2.+, S2.leg0, R2.Pin_1
