# Fritzing sketch id3016_PKE___3___18_0 (saved by Fritzing 0.9.2b)
breadboards: 1

parts:
  VCC1 = Battery block 9V
  R1 = Resistor [tolerance=±5% resistance=100k package=THT]
  T1 = NPN-Transistor [package="TO92 [THT]"]
  R2 = Resistor [tolerance=±5% resistance=2.2k package=THT]
  R9 = Resistor [tolerance=±5% resistance=10k package=THT]
  LED1 = LED - 5mm [color="Red (633nm)" package="5 mm [THT]"]
  C1 = Electrolytic Capacitor [capacitance=10µF package="100 mil [THT, electrolytic]"]
  S1 = Pushbutton [package=THT]
  R13 = Resistor [tolerance=±5% resistance=4.7k package=THT]
  R10 = Resistor [tolerance=±5% resistance=10k package=THT]
  R4 = Resistor [tolerance=±5% resistance=2.2k package=THT]
  R3 = Resistor [tolerance=±5% resistance=100k package=THT]
  T2 = NPN-Transistor [package="TO92 [THT]"]
  LED2 = LED - 5mm [color="Red (633nm)" package="5 mm [THT]"]
  C2 = Electrolytic Capacitor [capacitance=10µF package="100 mil [THT, electrolytic]"]
  R11 = Resistor [tolerance=±5% resistance=10k package=THT]
  R6 = Resistor [tolerance=±5% resistance=2.2k package=THT]
  R13_2 = Resistor [tolerance=±5% resistance=100k package=THT]
  T3 = NPN-Transistor [package="TO92 [THT]"]
  LED3 = LED - 5mm [color="Red (633nm)" package="5 mm [THT]"]
  C3 = Electrolytic Capacitor [capacitance=10µF package="100 mil [THT, electrolytic]"]
  R12 = Resistor [tolerance=±5% resistance=10k package=THT]
  R8 = Resistor [tolerance=±5% resistance=2.2k package=THT]
  R7 = Resistor [tolerance=±5% resistance=100k package=THT]
  T4 = NPN-Transistor [package="TO92 [THT]"]  # not connected
  LED4 = LED - 5mm [color="Red (633nm)" package="5 mm [THT]"]
  C4 = Electrolytic Capacitor [capacitance=10µF package="100 mil [THT, electrolytic]"]

nets:
  N1: VCC1.-, T1.E, S1.leg1, T2.E, T3.E
  N2: VCC1.+, R1.Pin_0, R9.Pin_0, LED1.anode, R13.Pin_0, R10.Pin_0, R3.Pin_0, LED2.anode, R11.Pin_0, R13_2.Pin_0, LED3.anode, R12.Pin_0, R7.Pin_0, LED4.anode
  N3: R1.Pin_1, T1.B, C1.-
  N4: T1.C, R2.Pin_1, C2.+
  N5: R2.Pin_0, R9.Pin_1, LED1.cathode
  N6: C1.+, S1.leg0, R13.Pin_1
  N7: R10.Pin_1, R4.Pin_0, LED2.cathode
  N8: R4.Pin_1, T2.C, C3.+
  N9: R3.Pin_1, T2.B, C2.-
  N10: R11.Pin_1, R6.Pin_0, LED3.cathode
  N11: R6.Pin_1, T3.C, C4.+
  N12: R13_2.Pin_1, T3.B, C3.-
  N13: R12.Pin_1, R8.Pin_0, LED4.cathode
  N14: R7.Pin_1, C4.-
