# Fritzing sketch id3017_PKE___3___19_0 (saved by Fritzing 0.9.2b)
breadboards: 1

parts:
  VCC1 = Battery block 9V
  R3 = Resistor [tolerance=±5% resistance=100k package=THT]
  R1 = Resistor [tolerance=±5% resistance=2.2k package=THT]
  R5 = Resistor [tolerance=±5% resistance=10k package=THT]
  LED1 = LED - 5mm [color="Red (635nm)" package="5 mm [THT]"]
  R4 = Resistor [tolerance=±5% resistance=100k package=THT]
  T2 = NPN-Transistor [package="TO92 [THT]"]
  R2 = Resistor [tolerance=±5% resistance=2.2k package=THT]
  LED2 = LED - 5mm [color="Red (635nm)" package="5 mm [THT]"]
  R6 = Resistor [tolerance=±5% resistance=10k package=THT]
  C2 = Electrolytic Capacitor [capacitance=10µF package="100 mil [THT, electrolytic]"]
  LEDB = LED - 5mm [color="White (6500K)" package="5 mm [THT]"]
  LEDA = LED - 5mm [color="White (6500K)" package="5 mm [THT]"]
  T1 = NPN-Transistor [package="TO92 [THT]"]
  C1 = Electrolytic Capacitor [capacitance=10µF package="100 mil [THT, electrolytic]"]

nets:
  N1: VCC1.-, T2.E, LEDB.anode, LEDA.anode, T1.E
  N2: VCC1.+, R3.Pin_0, R5.Pin_0, LED1.anode, R4.Pin_0, LED2.anode, R6.Pin_0
  N3: R3.Pin_1, LEDA.cathode, T1.B, C1.-
  N4: R1.Pin_0, R5.Pin_1, LED1.cathode
  N5: R1.Pin_1, C2.+, T1.C
  N6: R4.Pin_1, T2.B, C2.-, LEDB.cathode
  N7: T2.C, R2.Pin_1, C1.+
  N8: R2.Pin_0, LED2.cathode, R6.Pin_1
