# Fritzing sketch id3018_PKE___3___2_0 (saved by Fritzing 0.9.2b)
breadboards: 1

parts:
  LED1 = LED - 5mm [color="Yellow (585nm)" package="5 mm [THT]"]
  R1 = Resistor [tolerance=±5% resistance=2.2k package=THT]
  S1 = Pushbutton [package=THT]
  R8 = Resistor [tolerance=±5% resistance=10k package=THT]
  VCC1 = Battery block 9V
  R5 = Resistor [tolerance=±5% resistance=100k package=THT]
  T1 = NPN-Transistor [package="TO92 [THT]"]
  C1 = Electrolytic Capacitor [capacitance=0.1mF package="100 mil [THT, electrolytic]"]
  R2 = Resistor [tolerance=±5% resistance=2.2k package=THT]
  R9 = Resistor [tolerance=±5% resistance=10k package=THT]
  LED2 = LED - 5mm [color="Blue (430nm)" package="5 mm [THT]"]
  R6 = Resistor [tolerance=±5% resistance=100k package=THT]
  T2 = NPN-Transistor [package="TO92 [THT]"]
  C2 = Electrolytic Capacitor [capacitance=0.1mF package="100 mil [THT, electrolytic]"]
  R3 = Resistor [tolerance=±5% resistance=2.2k package=THT]
  LED3 = LED - 5mm [color="Red (635nm)" package="5 mm [THT]"]
  R10 = Resistor [tolerance=±5% resistance=10k package=THT]
  R7 = Resistor [tolerance=±5% resistance=100k package=THT]
  T3 = NPN-Transistor [package="TO92 [THT]"]
  C3 = Electrolytic Capacitor [capacitance=0.1mF package="100 mil [THT, electrolytic]"]
  R4 = Resistor [tolerance=±5% resistance=2.2k package=THT]
  LED4 = LED - 5mm [color="Green (555nm)" package="5 mm [THT]"]
  R11 = Resistor [tolerance=±5% resistance=10k package=THT]

nets:
  N1: LED1.cathode, R1.Pin_0, R8.Pin_1
  N2: LED1.anode, R8.Pin_0, VCC1.+, R9.Pin_0, LED2.anode, LED3.anode, R10.Pin_0, LED4.anode, R11.Pin_0
  N3: R1.Pin_1, S1.leg0, R5.Pin_0
  N4: S1.leg1, VCC1.-, T1.E, C1.-, T2.E, C2.-, T3.E, C3.-
  N5: R5.Pin_1, T1.B, C1.+
  N6: T1.C, R2.Pin_1, R6.Pin_0
  N7: R2.Pin_0, R9.Pin_1, LED2.cathode
  N8: R6.Pin_1, T2.B, C2.+
  N9: T2.C, R3.Pin_1, R7.Pin_0
  N10: R3.Pin_0, LED3.cathode, R10.Pin_1
  N11: R7.Pin_1, T3.B, C3.+
  N12: T3.C, R4.Pin_1
  N13: R4.Pin_0, LED4.cathode, R11.Pin_1
