# Fritzing sketch id3019_PKE___3___22_0 (saved by Fritzing 0.9.2b)
breadboards: 1

parts:
  VCC1 = Battery block 9V
  R3 = Resistor [tolerance=±5% resistance=10k package=THT]
  R1 = Resistor [tolerance=±5% resistance=2.2k package=THT]
  LED1 = LED - 5mm [color="Red (635nm)" package="5 mm [THT]"]
  R4 = Resistor [tolerance=±5% resistance=10k package=THT]
  T2 = NPN-Transistor [package="TO92 [THT]"]
  R2 = Resistor [tolerance=±5% resistance=2.2k package=THT]
  LED2 = LED - 5mm [color="Red (635nm)" package="5 mm [THT]"]
  C2 = Electrolytic Capacitor [capacitance=1µF package="100 mil [THT, electrolytic]"]
  T1 = NPN-Transistor [package="TO92 [THT]"]
  C1 = Electrolytic Capacitor [capacitance=1µF package="100 mil [THT, electrolytic]"]
  T3 = NPN-Transistor [package="TO92 [THT]"]
  R5 = Resistor [tolerance=±5% resistance=470 package=THT]
  FR = Photocell (LDR) [package=THT]
  Y1 = Piezo Speaker

nets:
  N1: VCC1.-, T2.E, T1.E, FR.pin_1
  N2: VCC1.+, LED1.anode, LED2.anode, T3.C, R5.Pin_0, Y1.pin2
  N3: R3.Pin_0, R4.Pin_0, T3.E
  N4: R3.Pin_1, T1.B, C1.-
  N5: R1.Pin_0, LED1.cathode
  N6: R1.Pin_1, C2.+, T1.C
  N7: R4.Pin_1, T2.B, C2.-
  N8: T2.C, R2.Pin_1, C1.+
  N9: R2.Pin_0, LED2.cathode, Y1.pin1
  N10: T3.B, R5.Pin_1, FR.pin_0
