# Fritzing sketch id3020_PKE___3___5_0 (saved by Fritzing 0.9.2b)
breadboards: 1

parts:
  VCC1 = Battery block 9V
  R3 = Resistor [tolerance=±5% resistance=100k package=THT]
  T1 = NPN-Transistor [package="TO92 [THT]"]
  R1 = Resistor [tolerance=±5% resistance=2.2k package=THT]
  R5 = Resistor [tolerance=±5% resistance=10k package=THT]
  LED1 = LED - 5mm [color="Green (555nm)" package="5 mm [THT]"]
  R4 = Resistor [tolerance=±5% resistance=100k package=THT]
  T2 = NPN-Transistor [package="TO92 [THT]"]
  R2 = Resistor [tolerance=±5% resistance=2.2k package=THT]
  LED2 = LED - 5mm [color="Red (635nm)" package="5 mm [THT]"]
  R6 = Resistor [tolerance=±5% resistance=10k package=THT]
  S1 = Pushbutton [package=THT]
  S2 = Pushbutton [package=THT]

nets:
  N1: VCC1.-, T1.E, T2.E, S1.leg1, S2.leg1
  N2: VCC1.+, R5.Pin_0, LED1.anode, LED2.anode, R6.Pin_0
  N3: R3.Pin_0, T2.C, R2.Pin_1
  N4: R3.Pin_1, T1.B, S1.leg0
  N5: T1.C, R1.Pin_1, R4.Pin_0
  N6: R1.Pin_0, R5.Pin_1, LED1.cathode
  N7: R4.Pin_1, T2.B, S2.leg0
  N8: R2.Pin_0, LED2.cathode, R6.Pin_1
