# Fritzing sketch id3021_PKE___3___Projekt_0 (saved by Fritzing 0.9.2b)
breadboards: 1

parts:
  VCC1 = Battery block 9V
  T1 = PNP-Transistor [package="TO92 [THT]"]
  C1 = Ceramic Capacitor [capacitance=10nF package="100 mil [THT, multilayer]"]
  LED1 = LED - 5mm [color="White (4500K)" package="5 mm [THT]"]
  R2 = Resistor [tolerance=±5% resistance=4.7k package=THT]
  R1 = Resistor [tolerance=±5% resistance=4.7k package=THT]
  R3 = Resistor [tolerance=±5% resistance=220k package=THT]
  T2 = PNP-Transistor [package="TO92 [THT]"]
  LED2 = LED - 5mm [color="Blue (430nm)" package="5 mm [THT]"]
  C2 = Ceramic Capacitor [capacitance=10nF package="100 mil [THT, multilayer]"]
  R6 = Resistor [tolerance=±5% resistance=4.7k package=THT]
  R5 = Resistor [tolerance=±5% resistance=4.7k package=THT]
  R4 = Resistor [tolerance=±5% resistance=470k package=THT]
  T3 = PNP-Transistor [package="TO92 [THT]"]
  C3 = Ceramic Capacitor [capacitance=100nF package="100 mil [THT, multilayer]"]
  C4 = Ceramic Capacitor [capacitance=100nF package="100 mil [THT, multilayer]"]
  LED3 = LED - 5mm [color="Green (555nm)" package="5 mm [THT]"]
  R7 = Resistor [tolerance=±5% resistance=2.2k package=THT]
  R8 = Resistor [tolerance=±5% resistance=100k package=THT]
  R9 = Resistor [tolerance=±5% resistance=220k package=THT]
  R10 = Resistor [tolerance=±5% resistance=2.2k package=THT]
  T4 = PNP-Transistor [package="TO92 [THT]"]
  LED4 = RGB LED - (4 legs) [package="5 mm [THT]"]
  T5 = NPN-Transistor [package="TO92 [THT]"]
  R11 = Resistor [tolerance=±5% resistance=2.2k package=THT]
  C5 = Ceramic Capacitor [capacitance=100nF package="100 mil [THT, multilayer]"]
  R12 = Resistor [tolerance=±5% resistance=100k package=THT]
  T6 = NPN-Transistor [package="TO92 [THT]"]
  C6 = Ceramic Capacitor [capacitance=100nF package="100 mil [THT, multilayer]"]
  R13 = Resistor [tolerance=±5% resistance=100k package=THT]
  LED5 = LED - 5mm [color="Red (635nm)" package="5 mm [THT]"]
  R14 = Resistor [tolerance=±5% resistance=2.2k package=THT]
  T7 = NPN-Transistor [package="TO92 [THT]"]
  T8 = NPN-Transistor [package="TO92 [THT]"]
  C8 = Ceramic Capacitor [capacitance=100nF package="100 mil [THT, multilayer]"]
  C7 = Ceramic Capacitor [capacitance=100nF package="100 mil [THT, multilayer]"]
  R15 = Resistor [tolerance=±5% resistance=1k package=THT]
  R16 = Resistor [tolerance=±5% resistance=1k package=THT]
  R17 = Resistor [tolerance=±5% resistance=220k package=THT]
  R18 = Resistor [tolerance=±5% resistance=100k package=THT]
  R19 = Resistor [tolerance=±5% resistance=1k package=THT]
  R20 = Resistor [tolerance=±5% resistance=1k package=THT]
  LED6 = LED - 5mm [color="Yellow (585nm)" package="5 mm [THT]"]
  C9 = Electrolytic Capacitor [capacitance=1mF package="200 mil [THT, electrolytic]"]

nets:
  N1: VCC1.-, R2.Pin_1, R1.Pin_1, R3.Pin_1, R6.Pin_1, R5.Pin_1, R4.Pin_1, R7.Pin_1, R8.Pin_1, R9.Pin_1, R10.Pin_1
  N2: VCC1.+, LED1.anode, LED2.anode, LED3.anode, LED4.common_anode
  N3: T1.E, LED1.cathode
  N4: T1.B, C2.0, R4.Pin_0
  N5: T1.C, C1.0, R2.Pin_0, R1.Pin_0
  N6: C1.1, R3.Pin_0, T2.B
  N7: T2.E, LED2.cathode
  N8: T2.C, C2.1, R6.Pin_0, R5.Pin_0
  N9: T3.E, LED3.cathode
  N10: T3.B, C4.0, R9.Pin_0
  N11: T3.C, C3.0, R7.Pin_0
  N12: C3.1, R8.Pin_0, T4.B
  N13: C4.1, R10.Pin_0, T4.C
  N14: T4.E, LED4.red_cathode
  N15: LED4.green_cathode, R11.Pin_0
  N16: LED4.blue_cathode, R12.Pin_0, R13.Pin_0, R16.Pin_0
  N17: T5.E, T6.E, T7.E, T8.E, C9.-
  N18: T5.B, C6.0, R13.Pin_1
  N19: T5.C, R11.Pin_1, C5.0
  N20: C5.1, R12.Pin_1, T6.B
  N21: T6.C, C6.1, R14.Pin_1
  N22: LED5.cathode, R14.Pin_0
  N23: LED5.anode, R17.Pin_0, R18.Pin_0, LED6.anode, C9.+
  N24: T7.B, C8.0, R18.Pin_1
  N25: T7.C, C7.1, R15.Pin_1
  N26: T8.B, C7.0, R17.Pin_1
  N27: T8.C, C8.1, R19.Pin_0
  N28: R15.Pin_0, R16.Pin_1
  N29: R19.Pin_1, R20.Pin_1
  N30: R20.Pin_0, LED6.cathode
