# Fritzing sketch id3022_PKE___4___13_0 (saved by Fritzing 0.9.3b)
breadboards: 1

parts:
  VCC1 = Battery block 9V
  R = Resistor [tolerance=±5% resistance=1k package=THT]
  LED1 = LED - 5mm [color="Red (633nm)" package="5 mm [THT]"]
  T2 = NPN-Transistor [package="TO92 [THT]"]
  R3 = Resistor [tolerance=±5% resistance=2.2k package=THT]
  R2 = Resistor [tolerance=±5% resistance=2.2k package=THT]
  T1 = NPN-Transistor [package="TO92 [THT]"]
  R1 = Resistor [tolerance=±5% resistance=2.2k package=THT]
  R1_2 = Resistor [tolerance=±5% resistance=1k package=THT]
  LED1_2 = LED - 5mm [color="Blue (470nm)" package="5 mm [THT]"]
  T1_2 = NPN-Transistor [package="TO92 [THT]"]
  R3_2 = Resistor [tolerance=±5% resistance=2.2k package=THT]
  T2_2 = PNP-Transistor [package="TO92 [THT]"]
  R2_2 = Resistor [tolerance=±5% resistance=2.2k package=THT]

nets:
  N1: VCC1.-, LED1.cathode, R3.Pin_1, LED1_2.cathode, R3_2.Pin_1
  N2: VCC1.+, R.Pin_0, T1.C, R1.Pin_0, R1_2.Pin_0, T2_2.E
  N3: R.Pin_1, LED1.anode, T2.E
  N4: T2.B, R3.Pin_0, R2.Pin_1
  N5: T2.C, T1.B, R1.Pin_1
  N6: R2.Pin_0, T1.E
  N7: R1_2.Pin_1, LED1_2.anode, T1_2.B
  N8: T1_2.E, R3_2.Pin_0, R2_2.Pin_1
  N9: T1_2.C, T2_2.B
  N10: T2_2.C, R2_2.Pin_0
