# Fritzing sketch id3023_PKE___4___21_0 (saved by Fritzing 0.9.3b)
breadboards: 1

parts:
  VCC1 = Battery block 9V
  T2 = NPN-Transistor [package="TO92 [THT]"]
  T1 = NPN-Transistor [package="TO92 [THT]"]
  R4 = Resistor [tolerance=±5% resistance=22k package=THT]
  R3 = Resistor [tolerance=±5% resistance=47k package=THT]
  T4 = NPN-Transistor [package="TO92 [THT]"]
  T3 = NPN-Transistor [package="TO92 [THT]"]
  R7 = Resistor [tolerance=±5% resistance=47k package=THT]
  R6 = Resistor [tolerance=±5% resistance=47k package=THT]
  C1 = Electrolytic Capacitor [capacitance=0.1mF package="100 mil [THT, electrolytic]"]
  C2 = Electrolytic Capacitor [capacitance=0.1mF package="100 mil [THT, electrolytic]"]
  C3 = Electrolytic Capacitor [capacitance=10µF package="100 mil [THT, electrolytic]"]
  C4 = Electrolytic Capacitor [capacitance=10µF package="100 mil [THT, electrolytic]"]
  R2 = Resistor [tolerance=±5% resistance=2.2k package=THT]
  C5 = Electrolytic Capacitor [capacitance=0.1mF package="100 mil [THT, electrolytic]"]
  R1 = Resistor [tolerance=±5% resistance=470 package=THT]
  LED_RGB = RGB LED - (4 legs) [package="5 mm [THT]"]
  R5 = Resistor [tolerance=±5% resistance=2.2k package=THT]
  R8 = Resistor [tolerance=±5% resistance=2.2k package=THT]
  Y1 = Piezo Speaker
  D1 = Rectifier Diode [part_number=1N4148 package="300 mil [THT]"]

nets:
  N1: VCC1.-, T2.E, T1.E
  N2: VCC1.+, R4.Pin_0, R3.Pin_0, R7.Pin_0, R6.Pin_0, R2.Pin_0, LED_RGB.common_anode, Y1.pin2, D1.cathode
  N3: T2.B, R3.Pin_1, C1.-
  N4: T2.C, T4.E, T3.E, C2.+
  N5: T1.B, R4.Pin_1, C2.-
  N6: T1.C, C1.+, R2.Pin_1, C5.-
  N7: T4.B, R6.Pin_1, C3.-
  N8: T4.C, C4.+, R8.Pin_0
  N9: T3.B, R7.Pin_1, C4.-
  N10: T3.C, C3.+, R5.Pin_1
  N11: C5.+, R1.Pin_1
  N12: R1.Pin_0, LED_RGB.red_cathode, D1.anode
  N13: LED_RGB.green_cathode, R5.Pin_0
  N14: LED_RGB.blue_cathode, R8.Pin_1, Y1.pin1
