# Fritzing sketch id3023_Untitled_Sketch (saved by Fritzing 0.6.3b)
breadboards: 1

parts:
  R1 = Resistor [tolerance=±5% resistance=100 package=THT]
  R2 = Resistor [tolerance=±5% resistance=220 package=THT]
  Q1 = NPN-Transistor [package="TO92 [THT]"]
  LASER = LED - 5mm [color="Red (633nm)" package="5 mm [THT]"]

nets:
  3.3V/GND: R1.Pin_0, R2.Pin_0, Q1.E
  N1: R1.Pin_1, LASER.anode
  N2: R2.Pin_1, Q1.B
  N3: Q1.C, LASER.cathode

notes:
  GPIO PIN
