# Fritzing sketch id3024_PKE___4___23_0 (saved by Fritzing 0.9.3b)
breadboards: 1

parts:
  VCC1 = Battery block 9V
  C3 = Electrolytic Capacitor [capacitance=0.1mF package="100 mil [THT, electrolytic]"]
  C4 = Electrolytic Capacitor [capacitance=0.1mF package="100 mil [THT, electrolytic]"]
  T1 = PNP-Transistor [package="TO92 [THT]"]
  R1 = Resistor [tolerance=±5% resistance=220k package=THT]
  S1 = Pushbutton [package=THT]
  C5 = Ceramic Capacitor [capacitance=1µF package="100 mil [THT, multilayer]"]
  R2 = Resistor [tolerance=±5% resistance=100k package=THT]
  R3 = Resistor [tolerance=±5% resistance=100k package=THT]
  T2 = PNP-Transistor [package="TO92 [THT]"]
  D1 = Rectifier Diode [part_number=1N4001 package="300 mil [THT]"]
  R4 = Resistor [tolerance=±5% resistance=10k package=THT]
  R5 = Resistor [tolerance=±5% resistance=22k package=THT]
  R6 = Resistor [tolerance=±5% resistance=10k package=THT]
  T3 = PNP-Transistor [package="TO92 [THT]"]
  R7 = Resistor [tolerance=±5% resistance=2.2k package=THT]
  T4 = NPN-Transistor [package="TO92 [THT]"]
  T5 = NPN-Transistor [package="TO92 [THT]"]
  T6 = NPN-Transistor [package="TO92 [THT]"]
  R8 = Resistor [tolerance=±5% resistance=10 package=THT]
  R9 = Resistor [tolerance=±5% resistance=10 package=THT]
  LED1 = LED - 5mm [color="White (6500K)" package="5 mm [THT]"]
  LED2 = LED - 5mm [color="White (6500K)" package="5 mm [THT]"]
  LED3 = LED - 5mm [color="Blue (470nm)" package="5 mm [THT]"]
  LED4 = LED - 5mm [color="Blue (470nm)" package="5 mm [THT]"]
  C1 = Electrolytic Capacitor [capacitance=1mF package="200 mil [THT, electrolytic]"]
  C2 = Electrolytic Capacitor [capacitance=1mF package="200 mil [THT, electrolytic]"]

nets:
  N1: VCC1.-, C3.-, C4.-, R1.Pin_1, R2.Pin_1, R4.Pin_1, T4.E, R8.Pin_1, R9.Pin_1, C1.-, C2.-
  N2: VCC1.+, D1.anode, R6.Pin_0, T3.E, LED1.anode, LED3.anode, C1.+, C2.+
  N3: C3.+, C4.+, T1.E, S1.leg1, T2.E, D1.cathode
  N4: T1.B, R3.Pin_0
  N5: T1.C, R1.Pin_0, S1.leg0, C5.1
  N6: C5.0, R2.Pin_0, T2.B
  N7: R3.Pin_1, T2.C, R4.Pin_0, R5.Pin_0
  N8: R5.Pin_1, R6.Pin_1, T3.B
  N9: T3.C, R7.Pin_0
  N10: R7.Pin_1, T4.C, T5.B, T6.B
  N11: T4.B, T5.E, R8.Pin_0
  N12: T5.C, LED2.cathode
  N13: T6.E, R9.Pin_0
  N14: T6.C, LED4.cathode
  N15: LED1.cathode, LED2.anode
  N16: LED3.cathode, LED4.anode
