# Fritzing sketch id3025_PKE___4___25_0 (saved by Fritzing 0.9.3b)
breadboards: 1

parts:
  VCC1 = Battery block 9V
  T1 = PNP-Transistor [package="TO92 [THT]"]
  R4 = Resistor [tolerance=±5% resistance=10k package=THT]
  R3 = Resistor [tolerance=±5% resistance=47k package=THT]
  R2 = Resistor [tolerance=±5% resistance=100k package=THT]
  R1 = Resistor [tolerance=±5% resistance=10k package=THT]
  T2 = PNP-Transistor [package="TO92 [THT]"]
  C1 = Electrolytic Capacitor [capacitance=0.1mF package="100 mil [THT, electrolytic]"]
  C2 = Electrolytic Capacitor [capacitance=0.1mF package="100 mil [THT, electrolytic]"]
  T3 = NPN-Transistor [package="TO92 [THT]"]
  LED3 = LED - 5mm [color="Red (633nm)" package="5 mm [THT]"]
  R5 = Resistor [tolerance=±5% resistance=4.7k package=THT]
  LED1 = LED - 5mm [color="Green (555nm)" package="5 mm [THT]"]
  S1 = Pushbutton [package=THT]
  D1 = Rectifier Diode [part_number=1N4001 package="300 mil [THT]"]
  C3 = Ceramic Capacitor [capacitance=100nF package="100 mil [THT, multilayer]"]
  T4 = PNP-Transistor [package="TO92 [THT]"]
  R7 = Resistor [tolerance=±5% resistance=1k package=THT]
  T5 = NPN-Transistor [package="TO92 [THT]"]
  R6 = Resistor [tolerance=±5% resistance=1k package=THT]
  LED2 = LED - 5mm [color="Green (555nm)" package="5 mm [THT]"]
  S2 = Pushbutton [package=THT]
  D2 = Rectifier Diode [part_number=1N4001 package="300 mil [THT]"]
  C4 = Ceramic Capacitor [capacitance=100nF package="100 mil [THT, multilayer]"]
  T4_2 = PNP-Transistor [package="TO92 [THT]"]
  R9 = Resistor [tolerance=±5% resistance=1k package=THT]
  T7 = NPN-Transistor [package="TO92 [THT]"]
  R8 = Resistor [tolerance=±5% resistance=1k package=THT]

nets:
  N1: VCC1.-, R4.Pin_1, R3.Pin_1, R2.Pin_1, R1.Pin_1, R5.Pin_1, C3.0, R7.Pin_1, T5.E, C4.0, R9.Pin_1, T7.E
  N2: VCC1.+, T1.E, T2.E, T3.C
  N3: T1.B, R3.Pin_0, C2.+
  N4: T1.C, R1.Pin_0, C1.-
  N5: R4.Pin_0, T2.C, C2.-, T3.B
  N6: R2.Pin_0, T2.B, C1.+
  N7: T3.E, LED3.anode, LED1.anode, LED2.anode
  N8: LED3.cathode, R5.Pin_0
  N9: LED1.cathode, S1.leg0, T4.E, R6.Pin_0
  N10: S1.leg1, D1.anode
  N11: D1.cathode, C3.1, T4.C, R7.Pin_0, T5.B
  N12: T4.B, T5.C, R6.Pin_1
  N13: LED2.cathode, S2.leg0, T4_2.E, R8.Pin_0
  N14: S2.leg1, D2.anode
  N15: D2.cathode, C4.1, T4_2.C, R9.Pin_0, T7.B
  N16: T4_2.B, T7.C, R8.Pin_1
