# Fritzing sketch id3026_PKE___4___7_0 (saved by Fritzing 0.9.3b)
breadboards: 1

parts:
  VCC1 = Battery block 9V
  R1 = Resistor [tolerance=±5% resistance=100k package=THT]
  R2 = Resistor [tolerance=±5% resistance=100k package=THT]
  R1_2 = Resistor [tolerance=±5% resistance=100k package=THT]
  R2_2 = Resistor [tolerance=±5% resistance=100k package=THT]
  R3 = Resistor [tolerance=±5% resistance=10k package=THT]
  R2_3 = Resistor [tolerance=±5% resistance=100k package=THT]
  R3_2 = Resistor [tolerance=±5% resistance=10k package=THT]
  R1_3 = Resistor [tolerance=±5% resistance=100k package=THT]
  T1 = NPN-Transistor [package="TO92 [THT]"]
  R1_4 = Resistor [tolerance=±5% resistance=100k package=THT]
  R2_4 = Resistor [tolerance=±5% resistance=100k package=THT]
  R3_3 = Resistor [tolerance=±5% resistance=10k package=THT]
  R4 = Resistor [tolerance=±5% resistance=100k package=THT]
  T1_2 = PNP-Transistor [package="TO92 [THT]"]
  T2 = NPN-Transistor [package="TO92 [THT]"]

nets:
  N1: VCC1.-, R2.Pin_1, R2_2.Pin_1, R3.Pin_1, R2_3.Pin_1, R3_2.Pin_1, R2_4.Pin_1, R3_3.Pin_1, T1_2.C
  N2: VCC1.+, R1.Pin_0, R1_2.Pin_0, R1_3.Pin_0, T1.C, R1_4.Pin_0, R4.Pin_0, T2.C
  N3: R1.Pin_1, R2.Pin_0
  N4: R1_2.Pin_1, R2_2.Pin_0, R3.Pin_0
  N5: R2_3.Pin_0, R1_3.Pin_1, T1.B
  N6: R3_2.Pin_0, T1.E
  N7: R1_4.Pin_1, R2_4.Pin_0, T1_2.B
  N8: R3_3.Pin_0, T2.E
  N9: R4.Pin_1, T1_2.E, T2.B
