# Fritzing sketch id3027_PKE___4___Projekt_0 (saved by Fritzing 0.9.3b)
breadboards: 1

parts:
  T1 = NPN-Transistor [package="TO92 [THT]"]
  T2 = NPN-Transistor [package="TO92 [THT]"]
  C1 = Ceramic Capacitor [capacitance=1µF package="100 mil [THT, multilayer]"]
  C2 = Ceramic Capacitor [capacitance=1µF package="100 mil [THT, multilayer]"]
  R1 = Resistor [tolerance=±5% resistance=470k package=THT]
  R2 = Resistor [tolerance=±5% resistance=4.7M package=THT]
  R3 = Resistor [tolerance=±5% resistance=10M package=THT]
  R4 = Resistor [tolerance=±5% resistance=470k package=THT]
  VCC1 = Battery block 9V
  C3 = Ceramic Capacitor [capacitance=10nF package="100 mil [THT, multilayer]"]
  R6 = Resistor [tolerance=±5% resistance=220k package=THT]
  R5 = Resistor [tolerance=±5% resistance=220k package=THT]
  T3 = PNP-Transistor [package="TO92 [THT]"]
  T4 = PNP-Transistor [package="TO92 [THT]"]
  R7 = Resistor [tolerance=±5% resistance=10M package=THT]
  FR = Photocell (LDR) [package=THT]
  T5 = NPN-Transistor [package="TO92 [THT]"]
  T6 = NPN-Transistor [package="TO92 [THT]"]
  J1 = Piezo Speaker
  R8 = Resistor [tolerance=±5% resistance=2.2k package=THT]

nets:
  N1: T1.E, T2.E, VCC1.-, FR.pin_0, T6.E
  N2: T1.B, C2.0, R3.Pin_1
  N3: T1.C, C1.0, R1.Pin_1
  N4: T2.B, C1.1, R2.Pin_1
  N5: T2.C, C2.1, R4.Pin_1, C3.0
  N6: R1.Pin_0, R2.Pin_0, R3.Pin_0, R4.Pin_0, VCC1.+, R5.Pin_0, T4.E
  N7: C3.1, R6.Pin_0
  N8: R6.Pin_1, R5.Pin_1, T3.B
  N9: T3.E, T4.B
  N10: T3.C, T4.C, R7.Pin_0, R8.Pin_0
  N11: R7.Pin_1, FR.pin_1, T5.B
  N12: T5.E, T6.B
  N13: T5.C, T6.C, J1.pin1
  N14: J1.pin2, R8.Pin_1
