# Fritzing sketch id3028_PKE___5___1_0 (saved by Fritzing 0.9.3b)
breadboards: 1

parts:
  LED2 = LED - 5mm [color="Red (633nm)" package="5 mm [THT]"]
  R1 = Resistor [tolerance=±5% resistance=1M package=THT]
  VCC1 = Battery block 9V
  T2 = NPN-Transistor [package="TO92 [THT]"]
  T1 = NPN-Transistor [package="TO92 [THT]"]
  LED1 = LED - 5mm [color="Red (633nm)" package="5 mm [THT]"]
  R1_2 = Resistor [tolerance=±5% resistance=47k package=THT]
  D1 = Rectifier Diode [part_number=1N4001 package="300 mil [THT]"]
  T1_2 = NPN-Transistor [package="TO92 [THT]"]
  LED1_2 = LED - 5mm [color="Yellow (585nm)" package="5 mm [THT]"]

nets:
  N1: LED2.cathode, R1.Pin_0
  N2: LED2.anode, VCC1.+, LED1.anode, R1_2.Pin_0, LED1_2.anode
  N3: R1.Pin_1, T2.B, T2.C, T1.B
  N4: VCC1.-, T2.E, T1.E, D1.cathode, T1_2.E
  N5: T1.C, LED1.cathode
  N6: R1_2.Pin_1, D1.anode, T1_2.B
  N7: T1_2.C, LED1_2.cathode
