# Fritzing sketch id3029_PKE___5___11_0 (saved by Fritzing 0.9.3b)
breadboards: 1

parts:
  VCC1 = Battery block 9V
  R1 = Resistor [tolerance=±5% resistance=22k package=THT]
  D1 = Rectifier Diode [part_number=1N4001 package="300 mil [THT]"]
  D3 = Rectifier Diode [part_number=1N4001 package="300 mil [THT]"]
  T1 = NPN-Transistor [package="TO92 [THT]"]
  R5 = Resistor [tolerance=±5% resistance=1k package=THT]
  T2 = NPN-Transistor [package="TO92 [THT]"]
  D4 = Rectifier Diode [part_number=1N4001 package="300 mil [THT]"]
  D2 = Rectifier Diode [part_number=1N4001 package="300 mil [THT]"]
  R2 = Resistor [tolerance=±5% resistance=22k package=THT]
  R3 = Resistor [tolerance=±5% resistance=2.2k package=THT]
  T3 = PNP-Transistor [package="TO92 [THT]"]
  LED1 = LED - 5mm [color="Red (635nm)" package="5 mm [THT]"]
  R4 = Resistor [tolerance=±5% resistance=1k package=THT]
  J1 = Piezo Speaker

nets:
  N1: VCC1.-, D1.cathode, D2.cathode, LED1.cathode, R4.Pin_1, J1.pin1
  N2: VCC1.+, R1.Pin_0, T1.C, R2.Pin_0, R3.Pin_0, T3.E
  N3: R1.Pin_1, D3.anode, T1.B
  N4: D1.anode, D3.cathode
  N5: T1.E, T2.E, R4.Pin_0
  N6: R5.Pin_0, T3.C
  N7: R5.Pin_1, LED1.anode, J1.pin2
  N8: T2.B, D4.anode, R2.Pin_1
  N9: T2.C, R3.Pin_1, T3.B
  N10: D4.cathode, D2.anode
