# Fritzing sketch id302_altimeter_0 (saved by Fritzing 0.7.7b)
breadboards: 1

parts:
  LCD1 = LCD screen
  Arduino1 = Arduino
  R1 = Trimmer Potentiometer [maximum_resistance=10kΩ package=THT]
  RE1 = Rotary Encoder [package=THT]
  S1 = Pushbutton [package="[THT]"]
  R3 = Resistor [tolerance=±5% resistance=220 package=THT]
  R4 = Resistor [tolerance=±5% resistance=220 package=THT]
  R5 = Resistor [tolerance=±5% resistance=220 package=THT]
  R7 = Resistor [tolerance=±5% resistance=220 package=THT]
  Part1 = Barometric Pressure Sensor - BMP085 Breakout
  S3 = Round Pushbutton

nets (from the breadboard view):
  GND: LCD1.VSS, LCD1.R/W, LCD1.LED-, Arduino1.GND, R1.leg1, RE1.EncoderPinB, S1.Pin_1, S1.Pin_2, Part1.GND, S3.leg1
  VDD: LCD1.VDD, LCD1.LED+, Arduino1.+5V
  N1: LCD1.V0, R1.wiper
  N2: LCD1.RS, Arduino1.D12
  N3: LCD1.E, Arduino1.D11
  N4: LCD1.DB4, Arduino1.D5
  N5: LCD1.DB5, Arduino1.D4
  N6: LCD1.DB6, Arduino1.D3
  N7: LCD1.DB7, Arduino1.D2
  N8: Arduino1.D10, S1.Pin_3, S1.Pin_4, R4.Pin_0
  N9: Arduino1.D9, RE1.EncoderPinC, R3.Pin_0
  N10: Arduino1.D8, RE1.EncoderPinA, R5.Pin_0
  N11: Arduino1.D7, R7.Pin_0, S3.leg0
  3V3: Arduino1.3V3, Part1.VCC
  N12: Arduino1.A4, Part1.SDA
  N13: Arduino1.A5, Part1.SCL
  N14: R1.leg2, R3.Pin_1, R4.Pin_1, R5.Pin_1, R7.Pin_1

notes:
  Pressure sensor
  Controls
  I2C
  Display
  5V
  3.3V
