# Fritzing sketch id3030_PKE___5___4_0 (saved by Fritzing 0.9.3b)
breadboards: 1

parts:
  R1 = Resistor [tolerance=±5% resistance=4.7k package=THT]
  VCC1 = Battery block 9V
  R2 = Resistor [tolerance=±5% resistance=2.2k package=THT]
  R3 = Resistor [tolerance=±5% resistance=100 package=THT]
  R4 = Resistor [tolerance=±5% resistance=2.2k package=THT]
  R5 = Resistor [tolerance=±5% resistance=10k package=THT]
  T1 = NPN-Transistor [package="TO92 [THT]"]
  LED1 = LED - 5mm [color="Red (633nm)" package="5 mm [THT]"]
  T2 = NPN-Transistor [package="TO92 [THT]"]
  LED2 = LED - 5mm [color="Red (633nm)" package="5 mm [THT]"]
  R6 = Resistor [tolerance=±5% resistance=470 package=THT]

nets:
  N1: R1.Pin_0, VCC1.+, LED1.anode, LED2.anode
  N2: R1.Pin_1, R2.Pin_0
  N3: VCC1.-, R4.Pin_1, R5.Pin_1, R6.Pin_1
  N4: R2.Pin_1, R3.Pin_0, R3.Pin_1, R4.Pin_0, R5.Pin_0, T1.B, T2.B
  N5: T1.E, T2.E, R6.Pin_0
  N6: T1.C, LED1.cathode
  N7: T2.C, LED2.cathode
