# Fritzing sketch id3031_PKE___5___6_0 (saved by Fritzing 0.9.3b)
breadboards: 1

parts:
  VCC1 = Battery block 9V
  R1 = Resistor [tolerance=±5% resistance=22k package=THT]
  D1 = Rectifier Diode [part_number=1N4001 package="300 mil [THT]"]
  D3 = Rectifier Diode [part_number=1N4001 package="300 mil [THT]"]
  T1 = NPN-Transistor [package="TO92 [THT]"]
  R3 = Resistor [tolerance=±5% resistance=10k package=THT]
  R5 = Resistor [tolerance=±5% resistance=1k package=THT]
  T2 = NPN-Transistor [package="TO92 [THT]"]
  D4 = Rectifier Diode [part_number=1N4001 package="300 mil [THT]"]
  D2 = Rectifier Diode [part_number=1N4001 package="300 mil [THT]"]
  R2 = Resistor [tolerance=±5% resistance=22k package=THT]
  R4 = Resistor [tolerance=±5% resistance=10k package=THT]
  T3 = PNP-Transistor [package="TO92 [THT]"]
  R6 = Resistor [tolerance=±5% resistance=1k package=THT]
  T4 = PNP-Transistor [package="TO92 [THT]"]
  LED1 = LED - 5mm [color="Green (555nm)" package="5 mm [THT]"]
  LED2 = LED - 5mm [color="Red (633nm)" package="5 mm [THT]"]

nets:
  N1: VCC1.-, D1.cathode, R5.Pin_1, D2.cathode, LED1.cathode, LED2.cathode
  N2: VCC1.+, R1.Pin_0, R3.Pin_0, R2.Pin_0, R4.Pin_0, R6.Pin_0
  N3: R1.Pin_1, D3.anode, T1.B
  N4: D1.anode, D3.cathode
  N5: T1.E, R5.Pin_0, T2.E
  N6: T1.C, R3.Pin_1, T3.B
  N7: T2.B, D4.anode, R2.Pin_1
  N8: T2.C, R4.Pin_1, T4.B
  N9: D4.cathode, D2.anode
  N10: T3.E, R6.Pin_1, T4.E
  N11: T3.C, LED1.anode
  N12: T4.C, LED2.anode
