# Fritzing sketch id3032_PKE___5___Projekt___Termometr_0 (saved by Fritzing 0.9.3b)
breadboards: 1

parts:
  VCC1 = Battery block 9V
  R8 = Resistor [tolerance=±5% resistance=4.7k package=THT]
  T7 = NPN-Transistor [package="TO92 [THT]"]
  R9 = Resistor [tolerance=±5% resistance=100k package=THT]
  R10 = Resistor [tolerance=±5% resistance=10k package=THT]
  R11 = Resistor [tolerance=±5% resistance=2.2k package=THT]
  T6 = PNP-Transistor [package="TO92 [THT]"]
  R5 = Resistor [tolerance=±5% resistance=75k package=THT]
  R6 = Resistor [tolerance=±5% resistance=100k package=THT]
  R7 = Resistor [tolerance=±5% resistance=22k package=THT]
  T3 = PNP-Transistor [package="TO92 [THT]"]
  R3 = Resistor [tolerance=±5% resistance=10k package=THT]
  T4 = NPN-Transistor [package="TO92 [THT]"]
  R4 = Resistor [tolerance=±5% resistance=47 package=THT]
  D2 = Rectifier Diode [part_number=1N4001 package="300 mil [THT]"]
  D3 = Rectifier Diode [part_number=1N4001 package="300 mil [THT]"]
  D4 = Rectifier Diode [part_number=1N4001 package="300 mil [THT]"]
  LED_RGB = RGB LED - (4 legs) [package="5 mm [THT]"]
  LED1 = LED - 5mm [color="Green (555nm)" package="5 mm [THT]"]
  T5 = NPN-Transistor [package="TO92 [THT]"]
  D1 = Rectifier Diode [part_number=1N4001 package="300 mil [THT]"]
  R2 = Resistor [tolerance=±5% resistance=4.7k package=THT]
  T2 = PNP-Transistor [package="TO92 [THT]"]
  T1 = PNP-Transistor [package="TO92 [THT]"]
  R1 = Resistor [tolerance=±5% resistance=100 package=THT]

nets:
  N1: VCC1.-, T7.E, R11.Pin_1, R6.Pin_1, R7.Pin_1, T3.C, D4.cathode
  N2: VCC1.+, R8.Pin_0, R5.Pin_0, R3.Pin_0, T2.E, R1.Pin_0
  N3: R8.Pin_1, T7.C, R9.Pin_1, T6.E
  N4: T7.B, R9.Pin_0, R10.Pin_1
  N5: R10.Pin_0, R11.Pin_0
  N6: T6.B, R5.Pin_1, R6.Pin_0
  N7: T6.C, R7.Pin_0, T3.B
  N8: T3.E, R3.Pin_1, T4.B, T5.E
  N9: T4.E, R4.Pin_0
  N10: T4.C, LED_RGB.blue_cathode
  N11: R4.Pin_1, D2.anode, LED1.cathode, D1.cathode
  N12: D2.cathode, D3.anode
  N13: D3.cathode, D4.anode
  N14: LED_RGB.red_cathode, T5.C
  N15: LED_RGB.common_anode, T1.C
  N16: LED_RGB.green_cathode, LED1.anode
  N17: T5.B, D1.anode, R2.Pin_1
  N18: R2.Pin_0, T2.C, T1.B
  N19: T2.B, T1.E, R1.Pin_1
