# Fritzing sketch id3033_PKE___5___Projekt___Wskaznik_0 (saved by Fritzing 0.9.3b)
breadboards: 1

parts:
  VCC1 = Battery block 9V
  T8 = PNP-Transistor [package="TO92 [THT]"]
  R11 = Resistor [tolerance=±5% resistance=100k package=THT]
  T7 = NPN-Transistor [package="TO92 [THT]"]
  C2 = Ceramic Capacitor [capacitance=1µF package="100 mil [THT, multilayer]"]
  R10 = Resistor [tolerance=±5% resistance=100k package=THT]
  R12 = Resistor [tolerance=±5% resistance=470k package=THT]
  R9 = Resistor [tolerance=±5% resistance=22k package=THT]
  R8 = Resistor [tolerance=±5% resistance=47k package=THT]
  T6 = NPN-Transistor [package="TO92 [THT]"]
  LED3 = LED - 5mm [color="White (6500K)" package="5 mm [THT]"]
  T3 = PNP-Transistor [package="TO92 [THT]"]
  C1 = Electrolytic Capacitor [capacitance=100µF package="100 mil [THT, electrolytic]"]
  R7 = Resistor [tolerance=±5% resistance=220k package=THT]
  D2 = Rectifier Diode [part_number=1N4001 package="300 mil [THT]"]
  R3 = Resistor [tolerance=±5% resistance=10k package=THT]
  T4 = NPN-Transistor [package="TO92 [THT]"]
  R4 = Resistor [tolerance=±5% resistance=100 package=THT]
  LED2 = LED - 5mm [color="Green (555nm)" package="5 mm [THT]"]
  T5 = NPN-Transistor [package="TO92 [THT]"]
  R6 = Resistor [tolerance=±5% resistance=100 package=THT]
  R5 = Resistor [tolerance=±5% resistance=47 package=THT]
  LED_RGB = RGB LED - (4 legs) [package="5 mm [THT]"]
  LED1 = LED - 5mm [color="Green (555nm)" package="5 mm [THT]"]
  D1 = Rectifier Diode [part_number=1N4001 package="300 mil [THT]"]
  T1 = PNP-Transistor [package="TO92 [THT]"]
  R1 = Resistor [tolerance=±5% resistance=100 package=THT]
  T2 = PNP-Transistor [package="TO92 [THT]"]
  R2 = Resistor [tolerance=±5% resistance=4.7k package=THT]

nets:
  N1: VCC1.-, T7.E, R12.Pin_1, R8.Pin_1, T6.E, T3.C, C1.-, LED2.cathode
  N2: VCC1.+, T8.E, R7.Pin_0, R3.Pin_0, R1.Pin_0, T2.E
  N3: T8.B, R11.Pin_0
  N4: T8.C, C2.1, R9.Pin_0
  N5: R11.Pin_1, T7.C
  N6: T7.B, R10.Pin_0, R12.Pin_0, LED3.cathode
  N7: C2.0, R10.Pin_1
  N8: R9.Pin_1, R8.Pin_0, T6.B
  N9: T6.C, LED3.anode, T3.B, C1.+, R7.Pin_1
  N10: T3.E, D2.cathode, R5.Pin_0
  N11: D2.anode, R3.Pin_1, T4.B
  N12: T4.E, R4.Pin_0
  N13: T4.C, LED_RGB.red_cathode
  N14: R4.Pin_1, LED2.anode, LED1.cathode, D1.cathode
  N15: T5.E, R6.Pin_1
  N16: T5.B, D1.anode, R2.Pin_1
  N17: T5.C, LED_RGB.blue_cathode
  N18: R6.Pin_0, R5.Pin_1
  N19: LED_RGB.common_anode, T1.C
  N20: LED_RGB.green_cathode, LED1.anode
  N21: T1.E, R1.Pin_1, T2.B
  N22: T1.B, T2.C, R2.Pin_0
