# Fritzing sketch id3034_PKE___6___1_0 (saved by Fritzing 0.9.3b)
breadboards: 1

parts:
  VCC1 = Battery block 9V
  LED1 = LED - 5mm [color="White (6500K)" package="5 mm [THT]"]
  LED2 = LED - 5mm [color="White (6500K)" package="5 mm [THT]"]
  LED3 = LED - 5mm [color="Blue (470nm)" package="5 mm [THT]"]
  LED4 = LED - 5mm [color="Blue (470nm)" package="5 mm [THT]"]
  LED5 = LED - 5mm [color="Green (555nm)" package="5 mm [THT]"]
  LED6 = LED - 5mm [color="Green (555nm)" package="5 mm [THT]"]
  S1 = Pushbutton [package=THT]
  D1 = Rectifier Diode [part_number=1N4001 package="300 mil [THT]"]
  C1 = Electrolytic Capacitor [capacitance=1mF package="100 mil [THT, electrolytic]"]
  R1 = Resistor [tolerance=±5% resistance=470 package=THT]
  R2 = Resistor [tolerance=±5% resistance=2.2k package=THT]
  LED1_2 = LED - 5mm [color="White (6500K)" package="5 mm [THT]"]
  LED2_2 = LED - 5mm [color="White (6500K)" package="5 mm [THT]"]
  LED3_2 = LED - 5mm [color="Blue (470nm)" package="5 mm [THT]"]
  LED4_2 = LED - 5mm [color="Blue (470nm)" package="5 mm [THT]"]
  LED5_2 = LED - 5mm [color="Green (555nm)" package="5 mm [THT]"]
  LED6_2 = LED - 5mm [color="Green (555nm)" package="5 mm [THT]"]
  S1_2 = Pushbutton [package=THT]
  T1 = NPN-Transistor [package="TO92 [THT]"]
  T2 = PNP-Transistor [package="TO92 [THT]"]
  R1_2 = Resistor [tolerance=±5% resistance=22k package=THT]
  D1_2 = Rectifier Diode [part_number=1N4001 package="300 mil [THT]"]
  C1_2 = Electrolytic Capacitor [capacitance=1mF package="100 mil [THT, electrolytic]"]
  R2_2 = Resistor [tolerance=±5% resistance=2.2k package=THT]
  LED1_3 = LED - 5mm [color="White (6500K)" package="5 mm [THT]"]
  LED2_3 = LED - 5mm [color="White (6500K)" package="5 mm [THT]"]
  LED3_3 = LED - 5mm [color="Blue (470nm)" package="5 mm [THT]"]
  LED4_3 = LED - 5mm [color="Blue (470nm)" package="5 mm [THT]"]
  LED5_3 = LED - 5mm [color="Green (555nm)" package="5 mm [THT]"]
  LED6_3 = LED - 5mm [color="Green (555nm)" package="5 mm [THT]"]

nets:
  N1: VCC1.-, LED6.cathode, R1.Pin_1, LED6_2.cathode, T2.C, R1_2.Pin_1, LED6_3.cathode
  N2: VCC1.+, LED1.anode, S1.leg1, D1.anode, S1_2.leg1, T1.C, D1_2.anode
  N3: LED1.cathode, LED2.anode
  N4: LED2.cathode, LED3.anode
  N5: LED3.cathode, LED4.anode
  N6: LED4.cathode, LED5.anode
  N7: LED5.cathode, LED6.anode
  N8: S1.leg0, C1.-, R1.Pin_0
  N9: D1.cathode, C1.+, R2.Pin_0
  N10: R2.Pin_1, LED1_2.anode
  N11: LED1_2.cathode, LED2_2.anode
  N12: LED2_2.cathode, LED3_2.anode
  N13: LED3_2.cathode, LED4_2.anode
  N14: LED4_2.cathode, LED5_2.anode
  N15: LED5_2.cathode, LED6_2.anode
  N16: S1_2.leg0, T1.B, T2.B, R1_2.Pin_0
  N17: T1.E, T2.E, C1_2.-
  N18: D1_2.cathode, C1_2.+, R2_2.Pin_0
  N19: R2_2.Pin_1, LED1_3.anode
  N20: LED1_3.cathode, LED2_3.anode
  N21: LED2_3.cathode, LED3_3.anode
  N22: LED3_3.cathode, LED4_3.anode
  N23: LED4_3.cathode, LED5_3.anode
  N24: LED5_3.cathode, LED6_3.anode

notes:
  a)
  b)
  c)
