# Fritzing sketch id3035_PKE___6___12_0 (saved by Fritzing 0.9.3b)
breadboards: 1

parts:
  VCC1 = Battery block 9V
  Q1 = NPN-Transistor [package="TO92 [THT]"]
  R2 = Resistor [tolerance=±5% resistance=22k package=THT]
  R1 = Resistor [tolerance=±5% resistance=4.7k package=THT]
  S1 = Pushbutton [package=THT]
  R3 = Resistor [tolerance=±5% resistance=2.2k package=THT]
  C1 = Electrolytic Capacitor [capacitance=0.1mF package="100 mil [THT, electrolytic]"]
  DS2Y-5-DC5V1 = DS2Y-5-DC5V [part_number=DS2Y-5-DC5V]
  D1 = Rectifier Diode [part_number=1N4001 package="300 mil [THT]"]
  D2 = Rectifier Diode [part_number=1N4001 package="300 mil [THT]"]
  Q2 = PNP-Transistor [package="TO92 [THT]"]
  R4 = Resistor [tolerance=±5% resistance=22k package=THT]

nets:
  N1: VCC1.-, Q1.E, R2.Pin_1, D1.cathode
  N2: VCC1.+, S1.leg1, R3.Pin_0, Q2.E
  N3: Q1.B, R2.Pin_0, R1.Pin_1
  N4: Q1.C, R3.Pin_1, C1.+, R4.Pin_0
  N5: R1.Pin_0, S1.leg0
  N6: C1.-, DS2Y-5-DC5V1.16_-, D1.anode, D2.anode
  N7: DS2Y-5-DC5V1.1_+, D2.cathode, Q2.C
  N8: Q2.B, R4.Pin_1
