# Fritzing sketch id3036_PKE___6___2_0 (saved by Fritzing 0.9.3b)
breadboards: 1

parts:
  T1 = PNP-Transistor [package="TO92 [THT]"]
  T2 = PNP-Transistor [package="TO92 [THT]"]
  C1 = Ceramic Capacitor [capacitance=100nF package="100 mil [THT, multilayer]"]
  C2 = Ceramic Capacitor [capacitance=100nF package="100 mil [THT, multilayer]"]
  R1 = Resistor [tolerance=±5% resistance=4.7k package=THT]
  R2 = Resistor [tolerance=±5% resistance=4.7k package=THT]
  R3 = Resistor [tolerance=±5% resistance=100k package=THT]
  R4 = Resistor [tolerance=±5% resistance=100k package=THT]
  T3 = NPN-Transistor [package="TO92 [THT]"]
  T4 = PNP-Transistor [package="TO92 [THT]"]
  VCC1 = Battery block 9V
  D1 = Rectifier Diode [part_number=1N4148 package="300 mil [THT]"]
  C3 = Electrolytic Capacitor [capacitance=0.1mF package="100 mil [THT, electrolytic]"]
  D2 = Rectifier Diode [part_number=1N4148 package="300 mil [THT]"]
  C1_2 = Electrolytic Capacitor [capacitance=1mF package="100 mil [THT, electrolytic]"]
  R5 = Resistor [tolerance=±5% resistance=2.2k package=THT]
  LED1 = LED - 5mm [color="White (6500K)" package="5 mm [THT]"]
  LED2 = LED - 5mm [color="White (6500K)" package="5 mm [THT]"]
  LED3 = LED - 5mm [color="Blue (505nm)" package="5 mm [THT]"]
  LED4 = LED - 5mm [color="Blue (505nm)" package="5 mm [THT]"]
  LED5 = LED - 5mm [color="Green (565nm)" package="5 mm [THT]"]
  LED6 = LED - 5mm [color="Green (565nm)" package="5 mm [THT]"]

nets:
  N1: T1.E, T2.E, T3.C, VCC1.+, D1.anode
  N2: T1.B, C2.1, R4.Pin_0
  N3: T1.C, C1.1, R1.Pin_0
  N4: T2.B, C1.0, R3.Pin_0
  N5: T2.C, C2.0, R2.Pin_0, T3.B, T4.B
  N6: R1.Pin_1, R2.Pin_1, R3.Pin_1, R4.Pin_1, T4.C, VCC1.-, C1_2.-, LED6.cathode
  N7: T3.E, T4.E, C3.-
  N8: D1.cathode, C3.+, D2.anode
  N9: D2.cathode, C1_2.+, R5.Pin_0
  N10: R5.Pin_1, LED1.anode
  N11: LED1.cathode, LED2.anode
  N12: LED2.cathode, LED3.anode
  N13: LED3.cathode, LED4.anode
  N14: LED4.cathode, LED5.anode
  N15: LED5.cathode, LED6.anode
