# Fritzing sketch id3037_PKE___6___23_0 (saved by Fritzing 0.9.3b)
breadboards: 1

parts:
  VCC1 = Battery block 9V
  Q1 = PNP-Transistor [package="TO92 [THT]"]
  R1 = Resistor [tolerance=±5% resistance=4.7k package=THT]
  C1 = Ceramic Capacitor [capacitance=10nF package="100 mil [THT, multilayer]"]
  R3 = Resistor [tolerance=±5% resistance=47k package=THT]
  Q2 = PNP-Transistor [package="TO92 [THT]"]
  C2 = Ceramic Capacitor [capacitance=10nF package="100 mil [THT, multilayer]"]
  R4 = Resistor [tolerance=±5% resistance=100k package=THT]
  R2 = Resistor [tolerance=±5% resistance=4.7k package=THT]
  R5 = Resistor [tolerance=±5% resistance=10k package=THT]
  LED1 = LED - 5mm [color="Blue (470nm)" package="5 mm [THT]"]
  Q3 = NPN-Transistor [package="TO92 [THT]"]
  DS2Y-5-DC5V1 = DS2Y-5-DC5V [part_number=DS2Y-5-DC5V]
  Q4 = NPN-Transistor [package="TO92 [THT]"]
  D1 = Rectifier Diode [part_number=1N4001 package="300 mil [THT]"]
  R8 = Resistor [tolerance=±5% resistance=22k package=THT]
  R7 = Resistor [tolerance=±5% resistance=47k package=THT]
  R6 = Resistor [tolerance=±5% resistance=22k package=THT]
  C3 = Electrolytic Capacitor [capacitance=0.1mF package="100 mil [THT, electrolytic]"]
  R9 = Resistor [tolerance=±5% resistance=1k package=THT]
  LED2 = LED - 5mm [color="White (6500K)" package="5 mm [THT]"]
  LED3 = LED - 5mm [color="White (6500K)" package="5 mm [THT]"]
  LED4 = LED - 5mm [color="Yellow (585nm)" package="5 mm [THT]"]
  LED5 = LED - 5mm [color="Yellow (585nm)" package="5 mm [THT]"]
  LED6 = LED - 5mm [color="Green (555nm)" package="5 mm [THT]"]
  LED7 = LED - 5mm [color="Green (555nm)" package="5 mm [THT]"]

nets:
  N1: VCC1.-, R1.Pin_1, R3.Pin_1, R4.Pin_1, R5.Pin_1, LED1.cathode, Q4.E, R6.Pin_1, C3.-, LED7.cathode
  N2: VCC1.+, Q1.E, Q2.E, DS2Y-5-DC5V1.1_+
  N3: Q1.B, C2.0, R4.Pin_0, Q3.C
  N4: Q1.C, R1.Pin_0, C1.0
  N5: C1.1, R3.Pin_0, Q2.B
  N6: Q2.C, C2.1, R2.Pin_0
  N7: R2.Pin_1, R5.Pin_0, Q4.B
  N8: LED1.anode, Q3.E
  N9: Q3.B, R7.Pin_1, R6.Pin_0
  N10: DS2Y-5-DC5V1.16_-, Q4.C, D1.anode
  N11: D1.cathode, R8.Pin_0, C3.+, R9.Pin_0
  N12: R8.Pin_1, R7.Pin_0
  N13: R9.Pin_1, LED2.anode
  N14: LED2.cathode, LED3.anode
  N15: LED3.cathode, LED4.anode
  N16: LED4.cathode, LED5.anode
  N17: LED5.cathode, LED6.anode
  N18: LED6.cathode, LED7.anode
