# Fritzing sketch id3038_PKE___6___7_0 (saved by Fritzing 0.9.3b)
breadboards: 1

parts:
  VCC1 = Battery block 9V
  REL = DS2Y-5-DC5V [part_number=DS2Y-5-DC5V]
  LED1 = LED - 5mm [color="Red (633nm)" package="5 mm [THT]"]
  LED2 = LED - 5mm [color="Green (555nm)" package="5 mm [THT]"]
  S1 = Pushbutton [package=THT]
  DS2Y-5-DC5V1 = DS2Y-5-DC5V [part_number=DS2Y-5-DC5V]
  S2 = Pushbutton [package=THT]
  D1 = Rectifier Diode [part_number=1N4001 package="300 mil [THT]"]
  LED3 = LED - 5mm [color="White (6500K)" package="5 mm [THT]"]
  LED4 = LED - 5mm [color="White (6500K)" package="5 mm [THT]"]
  LED5 = LED - 5mm [color="Blue (470nm)" package="5 mm [THT]"]
  LED6 = LED - 5mm [color="Blue (470nm)" package="5 mm [THT]"]
  LED7 = LED - 5mm [color="Green (555nm)" package="5 mm [THT]"]
  LED8 = LED - 5mm [color="Green (555nm)" package="5 mm [THT]"]

nets:
  N1: VCC1.-, S1.leg0, S2.leg1, LED8.cathode
  N2: VCC1.+, REL.16_-, LED1.cathode, DS2Y-5-DC5V1.16_-
  N3: REL.1_+, LED1.anode, LED2.anode
  N4: LED2.cathode, S1.leg1
  N5: DS2Y-5-DC5V1.1_+, S2.leg0, D1.anode
  N6: D1.cathode, LED3.anode
  N7: LED3.cathode, LED4.anode
  N8: LED4.cathode, LED5.anode
  N9: LED5.cathode, LED6.anode
  N10: LED6.cathode, LED7.anode
  N11: LED7.cathode, LED8.anode
