# Fritzing sketch id3039_PKE___6___Projekt_0 (saved by Fritzing 0.9.3b)
breadboards: 1

parts:
  VCC1 = Battery block 9V
  S1 = Pushbutton [package=THT]
  DS2Y-5-DC5V1 = DS2Y-5-DC5V [part_number=DS2Y-5-DC5V]
  LED1 = LED - 5mm [color="White (6500K)" package="5 mm [THT]"]
  LED2 = LED - 5mm [color="White (6500K)" package="5 mm [THT]"]
  LED3 = LED - 5mm [color="Blue (470nm)" package="5 mm [THT]"]
  LED4 = LED - 5mm [color="Blue (470nm)" package="5 mm [THT]"]
  LED5 = LED - 5mm [color="Green (560nm)" package="5 mm [THT]"]
  LED6 = LED - 5mm [color="Green (560nm)" package="5 mm [THT]"]
  LED7 = LED - 5mm [color="Yellow (595nm)" package="5 mm [THT]"]
  LED8 = LED - 5mm [color="Yellow (595nm)" package="5 mm [THT]"]
  LED9 = LED - 5mm [color="Red (635nm)" package="5 mm [THT]"]
  LED10 = LED - 5mm [color="Red (635nm)" package="5 mm [THT]"]

nets:
  N1: VCC1.-, DS2Y-5-DC5V1.16_-, LED10.anode
  N2: VCC1.+, S1.leg1
  N3: S1.leg0, DS2Y-5-DC5V1.6_N.C.
  N4: DS2Y-5-DC5V1.4_COM, DS2Y-5-DC5V1.1_+, LED1.cathode
  N5: LED1.anode, LED2.cathode
  N6: LED2.anode, LED3.cathode
  N7: LED3.anode, LED4.cathode
  N8: LED4.anode, LED5.cathode
  N9: LED5.anode, LED6.cathode
  N10: LED6.anode, LED7.cathode
  N11: LED7.anode, LED8.cathode
  N12: LED8.anode, LED9.cathode
  N13: LED9.anode, LED10.cathode
