# Fritzing sketch id303_AltoidsAmp_v01_0 (saved by Fritzing 0.7.11b)
breadboards: 2

parts:
  IC1 = IC, DIP package, 8 pins [chip_label=LM386]
  -Vcc1+ = Battery
  C1 = Electrolytic Capacitor [capacitance=10µF package="100 mil [THT, electrolytic]"]
  Boost1 = Toggle Switch [package=THT]
  C2 = Electrolytic Capacitor [capacitance=220µF package="100 mil [THT, electrolytic]"]
  -Out1+ = Loudspeaker
  C3 = Ceramic Capacitor [capacitance=0.1µF package="100 mil [THT, multilayer]"]
  Vol1 = Rotary Potentiometer (Small) [maximum_resistance=100kΩ]
  +In1- = female pin header, 2 pins [form="♀ (female)"]
  IC2 = IC, DIP package, 8 pins [chip_label=LM386]
  +Vcc2- = Battery
  C4 = Electrolytic Capacitor [capacitance=10µF package="100 mil [THT, electrolytic]"]
  Boost2 = Toggle Switch [package=THT]
  C5 = Electrolytic Capacitor [capacitance=220µF package="100 mil [THT, electrolytic]"]
  +Out1- = Loudspeaker
  C6 = Ceramic Capacitor [capacitance=0.1µF package="100 mil [THT, multilayer]"]
  Vol2 = Rotary Potentiometer (Small) [maximum_resistance=100kΩ]
  -In2+ = female pin header, 2 pins [form="♀ (female)"]
  gnd = female pin header, 1 pin [form="♀ (female)"]
  gnd_2 = female pin header, 1 pin [form="♀ (female)"]
  gnd_3 = female pin header, 1 pin [form="♀ (female)"]
  gnd_4 = female pin header, 1 pin [form="♀ (female)"]

nets:
  N1: IC1.pin1, Boost1.COM
  N2: IC1.pin2, IC1.pin4, -Vcc1+.-, -Out1+.pin1, Vol1.leg2, +In1-.pin2, gnd.pin1, gnd_3.pin1
  N3: IC1.pin3, C3.0
  N4: IC1.pin5, C2.+
  N5: IC1.pin6, -Vcc1+.+
  N6: IC1.pin8, C1.-
  N7: C1.+, Boost1.L2
  N8: C2.-, -Out1+.pin2
  N9: C3.1, Vol1.wiper
  N10: Vol1.leg1, +In1-.pin1
  N11: IC2.pin1, Boost2.COM
  N12: IC2.pin2, IC2.pin4, +Vcc2-.-, +Out1-.pin1, Vol2.leg2, -In2+.pin2, gnd_2.pin1, gnd_4.pin1
  N13: IC2.pin3, C6.0
  N14: IC2.pin5, C5.+
  N15: IC2.pin6, +Vcc2-.+
  N16: IC2.pin8, C4.-
  N17: C4.+, Boost2.L2
  N18: C5.-, +Out1-.pin2
  N19: C6.1, Vol2.wiper
  N20: Vol2.leg1, -In2+.pin1

notes:
  Schalter bewirkt Boost*200
  +Eingang-
  Boost *200
  left | right
  ---------------------------
  Altoids-Amp v01 17.11.2012
  ^^
