# Fritzing sketch id3040_PKE___7___1_0 (saved by Fritzing 0.9.3b)
breadboards: 1

parts:
  VCC1 = Battery block 9V
  R1 = Resistor [tolerance=±5% resistance=10M package=THT]
  C1 = Ceramic Capacitor [capacitance=10nF package="100 mil [THT, multilayer]"]
  Q1 = NPN-Transistor [package="TO92 [THT]"]
  Q2 = PNP-Transistor [package="TO92 [THT]"]
  Q3 = PNP-Transistor [package="TO92 [THT]"]
  R2 = Resistor [tolerance=±5% resistance=1k package=THT]
  LED1 = LED - 5mm [color="Blue (470nm)" package="5 mm [THT]"]
  J1 = Piezo Speaker
  X = female pin header, 1 pin [form="♀ (female)"]
  Y = female pin header, 1 pin [form="♀ (female)"]

nets:
  N1: VCC1.-, R1.Pin_1, C1.0, Q1.E, Q2.C, Q3.C
  N2: VCC1.+, LED1.anode, J1.pin2, Y.pin1
  N3: R1.Pin_0, C1.1, Q1.B, X.pin1
  N4: Q1.C, Q2.B
  N5: Q2.E, Q3.B
  N6: Q3.E, R2.Pin_1, J1.pin1
  N7: R2.Pin_0, LED1.cathode
