# Fritzing sketch id3042_PKE___7___15_0 (saved by Fritzing 0.9.3b)
breadboards: 1

parts:
  VCC1 = Battery block 9V
  Q1 = PNP-Transistor [package="TO92 [THT]"]
  R1 = Resistor [tolerance=±5% resistance=4.7k package=THT]
  C1 = Ceramic Capacitor [capacitance=1nF package="100 mil [THT, multilayer]"]
  R3 = Resistor [tolerance=±5% resistance=22k package=THT]
  Q2 = PNP-Transistor [package="TO92 [THT]"]
  C2 = Ceramic Capacitor [capacitance=1nF package="100 mil [THT, multilayer]"]
  R2 = Resistor [tolerance=±5% resistance=4.7k package=THT]
  R4 = Resistor [tolerance=±5% resistance=22k package=THT]
  C3 = Ceramic Capacitor [capacitance=10nF package="100 mil [THT, multilayer]"]
  R5 = Resistor [tolerance=±5% resistance=100k package=THT]
  R6 = Resistor [tolerance=±5% resistance=47k package=THT]
  R7 = Resistor [tolerance=±5% resistance=1k package=THT]
  C4 = Ceramic Capacitor [capacitance=10nF package="100 mil [THT, multilayer]"]
  Q4 = NPN-Transistor [package="TO92 [THT]"]
  R8 = Resistor [tolerance=±5% resistance=470k package=THT]
  R9 = Resistor [tolerance=±5% resistance=10k package=THT]
  R10 = Resistor [tolerance=±5% resistance=10k package=THT]
  Q5 = PNP-Transistor [package="TO92 [THT]"]
  C5 = Ceramic Capacitor [capacitance=1nF package="100 mil [THT, multilayer]"]
  R11 = Resistor [tolerance=±5% resistance=1k package=THT]
  LED1 = LED - 5mm [color="Blue (470nm)" package="5 mm [THT]"]
  C6 = Electrolytic Capacitor [capacitance=10µF package="100 mil [THT, electrolytic]"]
  J1 = Piezo Speaker
  Q3 = NPN-Transistor [package="TO92 [THT]"]

nets:
  N1: VCC1.-, R1.Pin_1, R3.Pin_1, R2.Pin_1, R4.Pin_1, R6.Pin_1, R7.Pin_1, Q4.E, R9.Pin_1, C5.1, LED1.cathode, J1.pin1
  N2: VCC1.+, Q1.E, Q2.E, R5.Pin_0, R8.Pin_0, R10.Pin_0, Q5.E, C6.+, Q3.C
  N3: Q1.B, C2.1, R4.Pin_0
  N4: Q1.C, R1.Pin_0, C1.0
  N5: C1.1, R3.Pin_0, Q2.B
  N6: Q2.C, C2.0, R2.Pin_0
  N7: C3.1, R5.Pin_1, R6.Pin_0, Q3.B
  N8: R7.Pin_0, C4.0, Q3.E
  N9: C4.1, Q4.B, R8.Pin_1, R9.Pin_0
  N10: Q4.C, R10.Pin_1, Q5.B, C5.0
  N11: Q5.C, R11.Pin_0, C6.-, J1.pin2
  N12: R11.Pin_1, LED1.anode
