# Fritzing sketch id3043_PKE___7___3_0 (saved by Fritzing 0.9.3b)
breadboards: 1

parts:
  VCC1 = Battery block 9V
  C1 = Ceramic Capacitor [capacitance=10nF package="100 mil [THT, multilayer]"]
  Q1 = NPN-Transistor [package="TO92 [THT]"]
  Q2 = PNP-Transistor [package="TO92 [THT]"]
  Q3 = PNP-Transistor [package="TO92 [THT]"]
  R2 = Resistor [tolerance=±5% resistance=1k package=THT]
  LED1 = LED - 5mm [color="Blue (470nm)" package="5 mm [THT]"]
  J1 = Piezo Speaker
  X = female pin header, 1 pin [form="♀ (female)"]
  D1 = Rectifier Diode [part_number=1N4001 package="300 mil [THT]"]

nets:
  N1: VCC1.-, Q1.E, Q2.C, Q3.C, D1.anode
  N2: VCC1.+, LED1.anode, J1.pin2
  N3: C1.0, Q1.B, D1.cathode
  N4: C1.1, X.pin1
  N5: Q1.C, Q2.B
  N6: Q2.E, Q3.B
  N7: Q3.E, R2.Pin_1, J1.pin1
  N8: R2.Pin_0, LED1.cathode
