# Fritzing sketch id3044_PKE___7___Projekt_0 (saved by Fritzing 0.9.3b)
breadboards: 1

parts:
  VCC1 = Battery block 9V
  Q1 = NPN-Transistor [package="TO92 [THT]"]
  Q2 = PNP-Transistor [package="TO92 [THT]"]
  Q3 = PNP-Transistor [package="TO92 [THT]"]
  R2 = Resistor [tolerance=±5% resistance=1k package=THT]
  LED1 = LED - 5mm [color="Blue (470nm)" package="5 mm [THT]"]
  J1 = Piezo Speaker
  X = female pin header, 1 pin [form="♀ (female)"]
  D1 = Rectifier Diode [part_number=1N4001 package="300 mil [THT]"]
  IC1 = IC, DIP package, 16 pins [chip_label=4017]
  R2_2 = Resistor [tolerance=±5% resistance=10k package=THT]
  LED2 = LED - 5mm [color="Red (633nm)" package="5 mm [THT]"]
  LED3 = LED - 5mm [color="Yellow (595nm)" package="5 mm [THT]"]
  LED4 = LED - 5mm [color="Green (555nm)" package="5 mm [THT]"]
  LED5 = LED - 5mm [color="Blue (470nm)" package="5 mm [THT]"]
  LED6 = LED - 5mm [color="White (6500K)" package="5 mm [THT]"]

nets:
  N1: VCC1.-, Q1.E, Q2.C, Q3.C, D1.anode, IC1.pin8, IC1.pin13, IC1.pin15, LED2.cathode, LED3.cathode, LED4.cathode, LED5.cathode, LED6.cathode
  N2: VCC1.+, LED1.anode, J1.pin2, IC1.pin16, R2_2.Pin_0
  N3: Q1.B, X.pin1, D1.cathode
  N4: Q1.C, Q2.B
  N5: Q2.E, Q3.B
  N6: Q3.E, R2.Pin_1, J1.pin1, IC1.pin14, R2_2.Pin_1
  N7: R2.Pin_0, LED1.cathode
  N8: IC1.pin3, LED2.anode
  N9: IC1.pin4, LED3.anode
  N10: IC1.pin5, LED5.anode
  N11: IC1.pin9, LED6.anode
  N12: IC1.pin10, LED4.anode
