# Fritzing sketch id3045_PKE___8___16_0 (saved by Fritzing 0.9.3b)
breadboards: 1

parts:
  VCC1 = Battery block 9V
  CX = Ceramic Capacitor [capacitance=1µF package="100 mil [THT, multilayer]"]
  RX = Resistor [tolerance=±5% resistance=100k package=THT]
  R1 = Resistor [tolerance=±5% resistance=100k package=THT]
  Q1 = NPN-Transistor [package="TO92 [THT]"]
  R4 = Resistor [tolerance=±5% resistance=22k package=THT]
  R3 = Resistor [tolerance=±5% resistance=22k package=THT]
  Q2 = NPN-Transistor [package="TO92 [THT]"]
  R2 = Resistor [tolerance=±5% resistance=4.7k package=THT]
  C1 = Electrolytic Capacitor [capacitance=1mF package="100 mil [THT, electrolytic]"]
  J1 = male pin header, 1 pin [form="♂ (male)"]

nets:
  N1: VCC1.-, CX.0, R4.Pin_1, C1.-
  N2: VCC1.+, R1.Pin_0, R2.Pin_0, C1.+
  N3: CX.1, RX.Pin_1, Q1.B
  N4: RX.Pin_0, R1.Pin_1, Q1.C, R3.Pin_0
  N5: Q1.E, R4.Pin_0, Q2.E
  N6: R3.Pin_1, Q2.B
  N7: Q2.C, R2.Pin_1, J1.pin1
