# Fritzing sketch id3046_PKE___8___18_0 (saved by Fritzing 0.9.3b)
breadboards: 1

parts:
  VCC1 = Battery block 9V
  Q5 = NPN-Transistor [package="TO92 [THT]"]
  R8 = Resistor [tolerance=±5% resistance=1k package=THT]
  LED1 = LED - 5mm [color="Yellow (585nm)" package="5 mm [THT]"]
  R7 = Resistor [tolerance=±5% resistance=10k package=THT]
  D1 = Rectifier Diode [part_number=1N4001 package="300 mil [THT]"]
  Q6 = PNP-Transistor [package="TO92 [THT]"]
  R6 = Resistor [tolerance=±5% resistance=1M package=THT]
  Cx = Electrolytic Capacitor [capacitance=10µF package="100 mil [THT, electrolytic]"]
  Q1 = NPN-Transistor [package="TO92 [THT]"]
  R4 = Resistor [tolerance=±5% resistance=10k package=THT]
  R3 = Resistor [tolerance=±5% resistance=100k package=THT]
  Q2 = NPN-Transistor [package="TO92 [THT]"]
  R1 = Resistor [tolerance=±5% resistance=100k package=THT]
  R2 = Resistor [tolerance=±5% resistance=1k package=THT]
  Q3 = PNP-Transistor [package="TO92 [THT]"]
  R5 = Resistor [tolerance=±5% resistance=2.2k package=THT]
  Rx = Resistor [tolerance=±5% resistance=100k package=THT]
  C1 = Electrolytic Capacitor [capacitance=1mF package="100 mil [THT, electrolytic]"]

nets:
  N1: VCC1.-, LED1.cathode, Q6.C, Cx.-, R4.Pin_1, R5.Pin_1, C1.-
  N2: VCC1.+, Q5.C, R7.Pin_0, R1.Pin_0, Q3.E, C1.+
  N3: Q5.E, R8.Pin_0
  N4: Q5.B, R7.Pin_1, D1.anode
  N5: R8.Pin_1, LED1.anode
  N6: D1.cathode, Q6.E
  N7: Q6.B, R6.Pin_0, Cx.+, Rx.Pin_1
  N8: R6.Pin_1, Q1.B
  N9: Q1.E, R4.Pin_0, Q2.E
  N10: Q1.C, R3.Pin_0, R1.Pin_1
  N11: R3.Pin_1, Q2.B
  N12: Q2.C, R2.Pin_1
  N13: R2.Pin_0, Q3.B
  N14: Q3.C, R5.Pin_0, Rx.Pin_0
