# Fritzing sketch id3047_PKE___8___20_0 (saved by Fritzing 0.9.3b)
breadboards: 1

parts:
  R7 = Resistor [tolerance=±5% resistance=22k package=THT]
  VCC1 = Battery block 9V
  Q4 = NPN-Transistor [package="TO92 [THT]"]
  Q5 = NPN-Transistor [package="TO92 [THT]"]
  Cx = Ceramic Capacitor [capacitance=1µF package="100 mil [THT, multilayer]"]
  R6 = Resistor [tolerance=±5% resistance=1M package=THT]
  Q1 = NPN-Transistor [package="TO92 [THT]"]
  R4 = Resistor [tolerance=±5% resistance=10k package=THT]
  R3 = Resistor [tolerance=±5% resistance=100k package=THT]
  R1 = Resistor [tolerance=±5% resistance=100k package=THT]
  Q2 = NPN-Transistor [package="TO92 [THT]"]
  R2 = Resistor [tolerance=±5% resistance=1k package=THT]
  R5 = Resistor [tolerance=±5% resistance=22k package=THT]
  Q3 = PNP-Transistor [package="TO92 [THT]"]
  C1 = Electrolytic Capacitor [capacitance=1mF package="100 mil [THT, electrolytic]"]
  Q4_2 = PNP-Transistor [package="TO92 [THT]"]
  R7_2 = Resistor [tolerance=±5% resistance=22k package=THT]
  Q5_2 = PNP-Transistor [package="TO92 [THT]"]
  Cx_2 = Ceramic Capacitor [capacitance=1µF package="100 mil [THT, multilayer]"]
  R6_2 = Resistor [tolerance=±5% resistance=1M package=THT]
  Q1_2 = PNP-Transistor [package="TO92 [THT]"]
  R1_2 = Resistor [tolerance=±5% resistance=100k package=THT]
  R4_2 = Resistor [tolerance=±5% resistance=10k package=THT]
  R3_2 = Resistor [tolerance=±5% resistance=100k package=THT]
  Q2_2 = PNP-Transistor [package="TO92 [THT]"]
  R2_2 = Resistor [tolerance=±5% resistance=1k package=THT]
  R5_2 = Resistor [tolerance=±5% resistance=22k package=THT]
  Q3_2 = NPN-Transistor [package="TO92 [THT]"]
  C1_2 = Electrolytic Capacitor [capacitance=1mF package="100 mil [THT, electrolytic]"]

nets:
  N1: R7.Pin_0, VCC1.+, Cx.1, R1.Pin_0, R5.Pin_0, Q3.E, C1.+, Q4_2.E, Q5_2.E, R4_2.Pin_0, C1_2.+
  N2: R7.Pin_1, Q4.B, Q4.C, Q5.B
  N3: VCC1.-, Q4.E, Q5.E, R4.Pin_1, C1.-, R7_2.Pin_1, Cx_2.0, R1_2.Pin_1, R5_2.Pin_1, Q3_2.E, C1_2.-
  N4: Q5.C, Cx.0, R6.Pin_0, Q3.C
  N5: R6.Pin_1, Q1.B
  N6: Q1.E, R4.Pin_0, Q2.E
  N7: Q1.C, R3.Pin_0, R1.Pin_1
  N8: R3.Pin_1, Q2.B
  N9: Q2.C, R2.Pin_1
  N10: R2.Pin_0, R5.Pin_1, Q3.B
  N11: Q4_2.B, Q4_2.C, R7_2.Pin_0, Q5_2.B
  N12: Q5_2.C, Cx_2.1, R6_2.Pin_0, Q3_2.C
  N13: R6_2.Pin_1, Q1_2.B
  N14: Q1_2.E, R4_2.Pin_1, Q2_2.E
  N15: Q1_2.C, R1_2.Pin_0, R3_2.Pin_0
  N16: R3_2.Pin_1, Q2_2.B
  N17: Q2_2.C, R2_2.Pin_0
  N18: R2_2.Pin_1, R5_2.Pin_0, Q3_2.B
