# Fritzing sketch id3048_PKE___8___23_0 (saved by Fritzing 0.9.3b)
breadboards: 1

parts:
  VCC1 = Battery block 9V
  R10 = Resistor [tolerance=±5% resistance=10k package=THT]
  Cx = Electrolytic Capacitor [capacitance=1µF package="100 mil [THT, electrolytic]"]
  Rx = Resistor [tolerance=±5% resistance=1M package=THT]
  R9 = Resistor [tolerance=±5% resistance=1M package=THT]
  D1 = Rectifier Diode [part_number=1N4001 package="300 mil [THT]"]
  Q4 = PNP-Transistor [package="TO92 [THT]"]
  R8 = Resistor [tolerance=±5% resistance=4.7k package=THT]
  R6 = Resistor [tolerance=±5% resistance=220k package=THT]
  R1 = Resistor [tolerance=±5% resistance=100k package=THT]
  Q1 = NPN-Transistor [package="TO92 [THT]"]
  R4 = Resistor [tolerance=±5% resistance=10k package=THT]
  LED1 = LED - 5mm [color="Yellow (585nm)" package="5 mm [THT]"]
  R3 = Resistor [tolerance=±5% resistance=100k package=THT]
  Q2 = NPN-Transistor [package="TO92 [THT]"]
  R2 = Resistor [tolerance=±5% resistance=1k package=THT]
  R5 = Resistor [tolerance=±5% resistance=22k package=THT]
  Q3 = PNP-Transistor [package="TO92 [THT]"]
  R7 = Resistor [tolerance=±5% resistance=4.7k package=THT]
  LED2 = LED - 5mm [color="Red (633nm)" package="5 mm [THT]"]
  C1 = Electrolytic Capacitor [capacitance=1mF package="100 mil [THT, electrolytic]"]

nets:
  N1: VCC1.-, R10.Pin_1, R9.Pin_1, D1.anode, R4.Pin_1, LED1.cathode, LED2.cathode, C1.-
  N2: VCC1.+, R10.Pin_0, Cx.+, Q4.E, R6.Pin_0, R5.Pin_0, Q3.E, C1.+
  N3: Cx.-, Rx.Pin_0, D1.cathode
  N4: Rx.Pin_1, R9.Pin_0, Q1.B
  N5: Q4.B, R6.Pin_1, R1.Pin_0
  N6: Q4.C, R8.Pin_0
  N7: R8.Pin_1, LED1.anode
  N8: R1.Pin_1, Q1.C, R3.Pin_0
  N9: Q1.E, R4.Pin_0, Q2.E
  N10: R3.Pin_1, Q2.B
  N11: Q2.C, R2.Pin_1
  N12: R2.Pin_0, R5.Pin_1, Q3.B
  N13: Q3.C, R7.Pin_0
  N14: R7.Pin_1, LED2.anode
