# Fritzing sketch id3049_PKE___8___9_0 (saved by Fritzing 0.9.3b)
breadboards: 1

parts:
  FR = Photocell (LDR) [package=THT]
  VCC1 = Battery block 9V
  R1 = Resistor [tolerance=±5% resistance=1k package=THT]  # not connected
  R2 = Resistor [tolerance=±5% resistance=10k package=THT]
  Q1 = NPN-Transistor [package="TO92 [THT]"]
  R3 = Resistor [tolerance=±5% resistance=4.7k package=THT]
  Q2 = NPN-Transistor [package="TO92 [THT]"]
  D1 = Rectifier Diode [part_number=1N4001 package="300 mil [THT]"]
  LED1 = LED - 5mm [color="Blue (470nm)" package="5 mm [THT]"]
  DS2Y-5-DC5V1 = DS2Y-5-DC5V [part_number=DS2Y-5-DC5V]
  R4 = Resistor [tolerance=±5% resistance=4.7k package=THT]
  LED2 = LED - 5mm [color="Green (555nm)" package="5 mm [THT]"]

nets:
  N1: FR.pin_0, R2.Pin_0
  N2: FR.pin_1, VCC1.+, R3.Pin_0, LED1.cathode, DS2Y-5-DC5V1.16_-, R4.Pin_0
  N3: VCC1.-, Q1.E, Q2.E, LED2.cathode
  N4: R2.Pin_1, Q1.B
  N5: Q1.C, R3.Pin_1, Q2.B
  N6: Q2.C, D1.anode, DS2Y-5-DC5V1.1_+
  N7: D1.cathode, LED1.anode
  N8: DS2Y-5-DC5V1.13_COM, R4.Pin_1
  N9: DS2Y-5-DC5V1.9_N.O., LED2.anode
