# Fritzing sketch id304_Amarino_Evaluation_Shield_0 (saved by Fritzing 0.7.10b)
breadboards: 2

parts:
  Arduino1 = Arduino
  LCD1 = LCD screen
  R2 = Trimmer Potentiometer [maximum_resistance=10kΩ package=THT]
  LED1 = RGB LED (com. cathode, rgb) [package="5 mm [THT]"]
  T1 = LM35 Temperature Sensor [package="TO92 [THT]"]
  R6 = Photocell (LDR) [package=THT]
  Part1 = Bluetooth Mate Silver
  R3 = 220 Ω Resistor [package=THT]
  R4 = 220 Ω Resistor [package=THT]
  R5 = 220 Ω Resistor [package=THT]
  R7 = 10k Ω Resistor [package=THT]
  S1 = Pushbutton [package="[THT]"]
  LED2 = white smd LED [package="0603 [SMD]"]
  R8 = 220 Ω Resistor [package=THT]

nets:
  N1: Arduino1.D13, LCD1.RS
  N2: Arduino1.D12, LCD1.E
  N3: Arduino1.D11, R8.Pin_0
  N4: Arduino1.D10, LCD1.DB4
  N5: Arduino1.D9, LCD1.DB5
  N6: Arduino1.D8, LCD1.DB6
  N7: Arduino1.D7, LCD1.DB7
  N8: Arduino1.D6, R4.Pin_0
  N9: Arduino1.D5, R5.Pin_0
  N10: Arduino1.D3, R3.Pin_0
  N11: Arduino1.D1TX, Part1.RX_5V
  N12: Arduino1.D0RX, Part1.TX_5V
  N13: Arduino1.RST, S1.Pin_1, S1.Pin_2
  +5V: Arduino1.+5V, LCD1.VDD, LCD1.LED+, T1.+Vs, R6.pin_0, Part1.VCC
  GND: Arduino1.GND, LCD1.VSS, LCD1.R/W, LCD1.LED-, R2.wiper, LED1.common_cathode, T1.GND, Part1.GND, R7.Pin_0, S1.Pin_3, S1.Pin_4, LED2.cathode
  N14: Arduino1.A0, R6.pin_1, R7.Pin_1
  N15: Arduino1.A1, T1.Vout
  N16: LCD1.V0, R2.leg2
  N17: LED1.red_anode, R3.Pin_1
  N18: LED1.green_anode, R4.Pin_1
  N19: LED1.blue_anode, R5.Pin_1
  N20: LED2.anode, R8.Pin_1

notes:
  Common cathode
  BlueSMiRF Mate Silver or any other adapter
  LM35
