# Fritzing sketch id3050_PKE___8___Projekt_0 (saved by Fritzing 0.9.3b)
breadboards: 1

parts:
  VCC1 = Battery block 9V
  R1 = Resistor [tolerance=±5% resistance=22k package=THT]
  R3 = Resistor [tolerance=±5% resistance=2.2k package=THT]
  D1 = Rectifier Diode [part_number=1N4001 package="300 mil [THT]"]
  Q5 = NPN-Transistor [package="TO92 [THT]"]
  R5 = Resistor [tolerance=±5% resistance=4.7k package=THT]
  Q6 = NPN-Transistor [package="TO92 [THT]"]
  Q1 = NPN-Transistor [package="TO92 [THT]"]
  Q2 = NPN-Transistor [package="TO92 [THT]"]
  Q3 = PNP-Transistor [package="TO92 [THT]"]
  Q4 = PNP-Transistor [package="TO92 [THT]"]
  R2 = Resistor [tolerance=±5% resistance=22k package=THT]
  R4 = Resistor [tolerance=±5% resistance=2.2k package=THT]
  D2 = Rectifier Diode [part_number=1N4001 package="300 mil [THT]"]
  Q7 = PNP-Transistor [package="TO92 [THT]"]
  Q8 = PNP-Transistor [package="TO92 [THT]"]
  R6 = Resistor [tolerance=±5% resistance=4.7k package=THT]
  R7 = Resistor [tolerance=±5% resistance=1k package=THT]
  R8 = Resistor [tolerance=±5% resistance=1k package=THT]
  LED1 = LED - 5mm [color="Red (633nm)" package="5 mm [THT]"]
  J1 = Piezo Speaker

nets:
  N1: VCC1.-, D1.cathode, Q5.E, Q6.E, D2.cathode, R7.Pin_1, R8.Pin_1, LED1.cathode, J1.pin1
  N2: VCC1.+, R1.Pin_0, R5.Pin_0, Q3.E, Q4.E, R2.Pin_0, Q8.E
  N3: R1.Pin_1, R3.Pin_0, Q1.B
  N4: R3.Pin_1, D1.anode
  N5: Q5.B, Q5.C, R5.Pin_1, Q6.B
  N6: Q6.C, Q1.E, Q2.E
  N7: Q1.C, Q3.B, Q3.C, Q4.B
  N8: Q2.B, R2.Pin_1, R4.Pin_0
  N9: Q2.C, Q4.C, Q7.B
  N10: R4.Pin_1, D2.anode
  N11: Q7.E, Q8.B
  N12: Q7.C, Q8.C, R6.Pin_1, R7.Pin_0, R8.Pin_0
  N13: R6.Pin_0, LED1.anode, J1.pin2
