# Fritzing sketch id3051_PKE___9___11_0 (saved by Fritzing 0.9.3b)
breadboards: 1

parts:
  VCC1 = Battery block 9V
  C1 = Electrolytic Capacitor [capacitance=100µF package="100 mil [THT, electrolytic]"]
  C3 = Ceramic Capacitor [capacitance=100nF package="100 mil [THT, multilayer]"]
  R3 = Resistor [tolerance=±5% resistance=10k package=THT]
  R4 = Resistor [tolerance=±5% resistance=10k package=THT]
  U1 = LM 358 Dual Op-Amp [package="DIP8 [THT]"]
  C4 = Ceramic Capacitor [capacitance=100nF package="100 mil [THT, multilayer]"]
  R6 = Resistor [tolerance=±5% resistance=47k package=THT]
  D1 = Rectifier Diode [part_number=1N4001 package="300 mil [THT]"]
  D2 = Rectifier Diode [part_number=1N4001 package="300 mil [THT]"]
  D3 = Rectifier Diode [part_number=1N4001 package="300 mil [THT]"]
  D4 = Rectifier Diode [part_number=1N4001 package="300 mil [THT]"]
  R5 = Resistor [tolerance=±5% resistance=22k package=THT]
  R1 = Resistor [tolerance=±5% resistance=4.7k package=THT]
  R7 = Resistor [tolerance=±5% resistance=22k package=THT]
  R2 = Resistor [tolerance=±5% resistance=4.7k package=THT]
  C2 = Electrolytic Capacitor [capacitance=1mF package="200 mil [THT, electrolytic]"]
  R8 = Resistor [tolerance=±5% resistance=2.2k package=THT]
  C5 = Electrolytic Capacitor [capacitance=100µF package="100 mil [THT, electrolytic]"]
  R9 = Resistor [tolerance=±5% resistance=1k package=THT]
  Z1 = Ceramic Capacitor [capacitance=1µF package="100 mil [THT, multilayer]"]
  Z2 = Resistor [tolerance=±5% resistance=1k package=THT]
  C1_2 = Electrolytic Capacitor [capacitance=0.1mF package="100 mil [THT, electrolytic]"]
  Q1 = PNP-Transistor [package="TO92 [THT]"]
  Q2 = PNP-Transistor [package="TO92 [THT]"]
  R10 = Resistor [tolerance=±5% resistance=10k package=THT]
  Q5 = NPN-Transistor [package="TO92 [THT]"]
  Q6 = NPN-Transistor [package="TO92 [THT]"]
  R12 = Resistor [tolerance=±5% resistance=100 package=THT]
  R14 = Resistor [tolerance=±5% resistance=470 package=THT]
  R16 = Resistor [tolerance=±5% resistance=4.7k package=THT]
  LED1 = LED - 5mm [color="Blue (470nm)" package="5 mm [THT]"]
  Q3 = PNP-Transistor [package="TO92 [THT]"]
  Q4 = PNP-Transistor [package="TO92 [THT]"]
  R11 = Resistor [tolerance=±5% resistance=10k package=THT]
  Q7 = NPN-Transistor [package="TO92 [THT]"]
  Q8 = NPN-Transistor [package="TO92 [THT]"]
  R13 = Resistor [tolerance=±5% resistance=100 package=THT]
  R15 = Resistor [tolerance=±5% resistance=470 package=THT]
  R17 = Resistor [tolerance=±5% resistance=4.7k package=THT]
  LED2 = LED - 5mm [color="Blue (470nm)" package="5 mm [THT]"]
  R18 = Resistor [tolerance=±5% resistance=2.2k package=THT]

nets:
  N1: VCC1.-, C1.-, U1.connector3, R2.Pin_1, C2.-, R9.Pin_1, Z2.Pin_1, C1_2.-, Q1.C, Q2.C, R12.Pin_0, Q3.C, Q4.C, R13.Pin_0
  N2: VCC1.+, C1.+, U1.connector7, R1.Pin_1, C1_2.+, R10.Pin_0, R16.Pin_0, LED1.anode, R11.Pin_0, LED2.anode, R18.Pin_1
  N3: C3.0, R3.Pin_0, R4.Pin_0, U1.connector4
  N4: C3.1, R3.Pin_1, R5.Pin_1, R1.Pin_0, R7.Pin_1, R2.Pin_0, C2.+
  N5: R4.Pin_1, C4.1
  N6: U1.connector0, R8.Pin_1, C5.-
  N7: U1.connector1, R7.Pin_0, R8.Pin_0
  N8: U1.connector2, U1.connector6, C4.0, R6.Pin_0, D1.cathode, D2.anode
  N9: U1.connector5, R6.Pin_1, D3.anode, D4.cathode, R5.Pin_0
  N10: D1.anode, D2.cathode, D3.cathode, D4.anode
  N11: C5.+, R9.Pin_0, Z1.1, Q1.B
  N12: Z1.0, Z2.Pin_0, Q3.B
  N13: Q1.E, Q2.B
  N14: Q2.E, R10.Pin_1, Q5.B
  N15: Q5.E, Q6.B
  N16: Q5.C, Q6.C, R14.Pin_0
  N17: Q6.E, R12.Pin_1
  N18: R14.Pin_1, R16.Pin_1, LED1.cathode
  N19: Q3.E, Q4.B
  N20: Q4.E, R11.Pin_1, Q7.B
  N21: Q7.E, Q8.B
  N22: Q7.C, Q8.C, R15.Pin_0
  N23: Q8.E, R13.Pin_1
  N24: R15.Pin_1, R17.Pin_1, LED2.cathode
  N25: R17.Pin_0, R18.Pin_0
