# Fritzing sketch id3052_PKE___9___16_0 (saved by Fritzing 0.9.3b)
breadboards: 1

parts:
  VCC1 = Battery block 9V
  R1 = Resistor [tolerance=±5% resistance=2.2k package=THT]
  R2 = Resistor [tolerance=±5% resistance=2.2k package=THT]
  MIC1 = Microphone
  C1 = Electrolytic Capacitor [capacitance=0.1mF package="100 mil [THT, electrolytic]"]
  C2 = Ceramic Capacitor [capacitance=100nF package="100 mil [THT, multilayer]"]
  R3 = Resistor [tolerance=±5% resistance=100k package=THT]
  R4 = Resistor [tolerance=±5% resistance=47k package=THT]
  Q1 = NPN-Transistor [package="TO92 [THT]"]
  R5 = Resistor [tolerance=±5% resistance=10k package=THT]
  R6 = Resistor [tolerance=±5% resistance=10k package=THT]
  C3 = Electrolytic Capacitor [capacitance=10µF package="100 mil [THT, electrolytic]"]
  R7 = Resistor [tolerance=±5% resistance=1k package=THT]
  Q2 = PNP-Transistor [package="TO92 [THT]"]
  R9 = Resistor [tolerance=±5% resistance=2.2k package=THT]
  R8 = Resistor [tolerance=±5% resistance=2.2k package=THT]
  R10 = Resistor [tolerance=±5% resistance=220 package=THT]
  C4 = Electrolytic Capacitor [capacitance=0.1mF package="100 mil [THT, electrolytic]"]
  Q3 = PNP-Transistor [package="TO92 [THT]"]
  R11 = Resistor [tolerance=±5% resistance=1k package=THT]
  C5 = Electrolytic Capacitor [capacitance=10µF package="100 mil [THT, electrolytic]"]
  R12 = Resistor [tolerance=±5% resistance=100k package=THT]
  C6 = Electrolytic Capacitor [capacitance=0.1mF package="100 mil [THT, electrolytic]"]

nets:
  N1: VCC1.-, MIC1.pin1, C1.-, R4.Pin_1, R6.Pin_1, R7.Pin_1, R8.Pin_1, Q3.C, R12.Pin_1, C6.-
  N2: VCC1.+, R1.Pin_0, R3.Pin_0, R5.Pin_0, R9.Pin_0, R10.Pin_0, R11.Pin_0, C6.+
  N3: R1.Pin_1, R2.Pin_0, C1.+
  N4: R2.Pin_1, MIC1.pin2, C2.0
  N5: C2.1, R3.Pin_1, R4.Pin_0, Q1.B
  N6: Q1.E, R6.Pin_0, C3.+
  N7: Q1.C, R5.Pin_1, Q2.B
  N8: C3.-, R7.Pin_0
  N9: Q2.E, R9.Pin_1, C4.-
  N10: Q2.C, R8.Pin_0, Q3.B
  N11: R10.Pin_1, C4.+
  N12: Q3.E, R11.Pin_1, C5.+
  N13: C5.-, R12.Pin_0
