# Fritzing sketch id3053_PKE___9___19_0 (saved by Fritzing 0.9.3b)
breadboards: 1

parts:
  VCC1 = Battery block 9V
  SPKR1 = Loudspeaker
  C1 = Electrolytic Capacitor [capacitance=0.1mF package="100 mil [THT, electrolytic]"]
  Q1 = NPN-Transistor [package="TO92 [THT]"]
  R2 = Resistor [tolerance=±5% resistance=10k package=THT]
  R1 = Resistor [tolerance=±5% resistance=10k package=THT]
  R3 = Resistor [tolerance=±5% resistance=100k package=THT]
  R4 = Resistor [tolerance=±5% resistance=47k package=THT]
  C2 = Electrolytic Capacitor [capacitance=10µF package="100 mil [THT, electrolytic]"]
  Q2 = PNP-Transistor [package="TO92 [THT]"]
  R6 = Resistor [tolerance=±5% resistance=1k package=THT]
  R5 = Resistor [tolerance=±5% resistance=1k package=THT]
  C3 = Electrolytic Capacitor [capacitance=0.1mF package="100 mil [THT, electrolytic]"]
  R7 = Resistor [tolerance=±5% resistance=22 package=THT]
  C4 = Electrolytic Capacitor [capacitance=10µF package="100 mil [THT, electrolytic]"]
  R8 = Resistor [tolerance=±5% resistance=100k package=THT]

nets:
  N1: VCC1.-, SPKR1.pin1, R2.Pin_1, R4.Pin_1, C2.-, R5.Pin_1, R8.Pin_1
  N2: VCC1.+, R1.Pin_0, R3.Pin_0, R6.Pin_0, R7.Pin_0
  N3: SPKR1.pin2, C1.-
  N4: C1.+, Q1.E, R2.Pin_0
  N5: Q1.B, R3.Pin_1, R4.Pin_0, C2.+
  N6: Q1.C, R1.Pin_1, Q2.B
  N7: Q2.E, R6.Pin_1, C3.-
  N8: Q2.C, R5.Pin_0, C4.+
  N9: C3.+, R7.Pin_1
  N10: C4.-, R8.Pin_0
