# Fritzing sketch id3054_PKE___9___30_0 (saved by Fritzing 0.9.3b)
breadboards: 1

parts:
  VCC1 = Battery block 9V
  R8 = Resistor [tolerance=±5% resistance=2.2k package=THT]
  R1 = Resistor [tolerance=±5% resistance=100k package=THT]
  R2 = Resistor [tolerance=±5% resistance=100k package=THT]
  C1 = Ceramic Capacitor [capacitance=100nF package="100 mil [THT, multilayer]"]
  R9 = Resistor [tolerance=±5% resistance=4.7k package=THT]
  C5 = Electrolytic Capacitor [capacitance=0.1mF package="100 mil [THT, electrolytic]"]
  Q1 = NPN-Transistor [package="TO92 [THT]"]
  R3 = Resistor [tolerance=±5% resistance=10k package=THT]
  C2 = Electrolytic Capacitor [capacitance=0.1mF package="100 mil [THT, electrolytic]"]
  R5 = Resistor [tolerance=±5% resistance=100 package=THT]
  R4 = Resistor [tolerance=±5% resistance=10k package=THT]
  Q2 = PNP-Transistor [package="TO92 [THT]"]
  R6 = Resistor [tolerance=±5% resistance=2.2k package=THT]
  C3 = Electrolytic Capacitor [capacitance=10µF package="100 mil [THT, electrolytic]"]
  R7 = Resistor [tolerance=±5% resistance=47k package=THT]
  C4 = Electrolytic Capacitor [capacitance=0.1mF package="100 mil [THT, electrolytic]"]
  MIC1 = Microphone

nets:
  N1: VCC1.-, R2.Pin_1, C5.-, R5.Pin_1, R6.Pin_1, R7.Pin_1, C4.-, MIC1.pin1
  N2: VCC1.+, R8.Pin_0, R3.Pin_0, Q2.E, C4.+
  N3: R8.Pin_1, R1.Pin_0, R9.Pin_0, C5.+
  N4: R1.Pin_1, R2.Pin_0, C1.1, Q1.B
  N5: C1.0, R9.Pin_1, MIC1.pin2
  N6: Q1.E, C2.+, R4.Pin_0
  N7: Q1.C, R3.Pin_1, Q2.B
  N8: C2.-, R5.Pin_0
  N9: R4.Pin_1, Q2.C, R6.Pin_0, C3.+
  N10: C3.-, R7.Pin_0
