# Fritzing sketch id3055_PKE___9___Projekt_0 (saved by Fritzing 0.9.3b)
breadboards: 1

parts:
  VCC1 = Battery block 9V
  MIC1 = Microphone
  R1 = Resistor [tolerance=±5% resistance=10k package=THT]
  C1 = Ceramic Capacitor [capacitance=100nF package="100 mil [THT, multilayer]"]
  R2 = Resistor [tolerance=±5% resistance=100k package=THT]
  R6 = Resistor [tolerance=±5% resistance=47k package=THT]
  Q1 = NPN-Transistor [package="TO92 [THT]"]
  R3 = Resistor [tolerance=±5% resistance=100k package=THT]
  C2 = Ceramic Capacitor [capacitance=100nF package="100 mil [THT, multilayer]"]
  R4 = Resistor [tolerance=±5% resistance=100k package=THT]
  Q3 = PNP-Transistor [package="TO92 [THT]"]
  R7 = Resistor [tolerance=±5% resistance=10M package=THT]
  C4 = Ceramic Capacitor [capacitance=100nF package="100 mil [THT, multilayer]"]
  Q2 = NPN-Transistor [package="TO92 [THT]"]
  R8 = Resistor [tolerance=±5% resistance=47k package=THT]
  C5 = Electrolytic Capacitor [capacitance=0.1mF package="100 mil [THT, electrolytic]"]
  IC1 = IC, DIP package, 16 pins [chip_label=4017]
  C3 = Ceramic Capacitor [capacitance=10nF package="100 mil [THT, multilayer]"]
  R5 = Resistor [tolerance=±5% resistance=220k package=THT]
  LED1 = RGB LED - (4 legs) [package="5 mm [THT]"]
  R9 = Resistor [tolerance=±5% resistance=4.7k package=THT]
  R10 = Resistor [tolerance=±5% resistance=4.7k package=THT]
  Q4 = PNP-Transistor [package="TO92 [THT]"]
  R11 = Resistor [tolerance=±5% resistance=4.7k package=THT]
  DS2Y-5-DC5V1 = DS2Y-5-DC5V [part_number=DS2Y-5-DC5V]
  D1 = Rectifier Diode [part_number=1N4001 package="300 mil [THT]"]

nets:
  N1: VCC1.-, MIC1.pin1, R6.Pin_1, C2.0, R7.Pin_0, C4.0, R8.Pin_1, C5.-, IC1.pin8, IC1.pin13, DS2Y-5-DC5V1.1_+, D1.anode
  N2: VCC1.+, R1.Pin_0, R2.Pin_0, R3.Pin_0, Q3.E, Q2.C, C5.+, IC1.pin16, C3.1, LED1.common_anode, Q4.E
  N3: MIC1.pin2, R1.Pin_1, C1.0
  N4: C1.1, R2.Pin_1, R6.Pin_0, Q1.B
  N5: Q1.E, C2.1, R4.Pin_0
  N6: Q1.C, R3.Pin_1, Q3.B
  N7: R4.Pin_1, Q2.E, R8.Pin_0, IC1.pin14
  N8: Q3.C, R7.Pin_1, C4.1, Q2.B
  N9: IC1.pin2, R10.Pin_1
  N10: IC1.pin3, R9.Pin_1, R11.Pin_1
  N11: IC1.pin4, R5.Pin_1
  N12: IC1.pin15, C3.0, R5.Pin_0
  N13: LED1.red_cathode, R9.Pin_0
  N14: LED1.green_cathode, R10.Pin_0
  N15: Q4.B, R11.Pin_0
  N16: Q4.C, DS2Y-5-DC5V1.16_-, D1.cathode
