# Fritzing sketch id3056_placa_desconhecida_0 (saved by Fritzing 0.7.12b)

parts:
  R25 = 4.7k Ω Resistor [package=THT]
  D2 = Rectifier Diode
  C10 = Ceramic Disk Capacitor [package=THT]
  D7 = Rectifier Diode
  R18 = 4.7k Ω Resistor [package=THT]
  D3 = Rectifier Diode
  R26 = 4.7k Ω Resistor [package=THT]
  C6 = Electrolytic Capacitor [package=THT]
  D5 = Rectifier Diode
  R24 = 4.7k Ω Resistor [package=THT]
  R19 = 4.7k Ω Resistor [package=THT]
  Power_plug1 = Power plug
  Componente1 = DB25M.fzp
  R28 = 4.7k Ω Resistor [package=THT]
  R17 = 4.7k Ω Resistor [package=THT]
  R22 = 4.7k Ω Resistor [package=THT]
  D10 = Rectifier Diode
  D12 = Rectifier Diode
  D1 = Rectifier Diode
  C9 = Ceramic Capacitor [package=THT]
  R20 = 4.7k Ω Resistor [package=THT]
  R21 = 4.7k Ω Resistor [package=THT]
  S1 = Pushbutton [package=THT]
  U2 = Optocoupler [package=THT]
  C4 = Electrolytic Capacitor [package=THT]
  R27 = 4.7k Ω Resistor [package=THT]
  D4 = Rectifier Diode
  C11 = Ceramic Disk Capacitor [package=THT]
  S3 = Toggle Switch [package=THT]
  XTAL1 = Crystal [frequency="16 Mhz" package=THT]
  C2 = Electrolytic Capacitor [package=THT]
  Power_plug2 = Power plug
  Componente2 = DB25M.fzp
  S2 = Toggle Switch [package=THT]
  R14 = 47k Ω Resistor [package=THT]
  D11 = Rectifier Diode
  C7 = Ceramic Capacitor [package=THT]
  C5 = Electrolytic Capacitor [package=THT]
  IC2 = ULN2003A [package="SO16 [SMD]"]
  R16 = 470 Ω Resistor [package=THT]
  PIC_16F877A1 = PIC_16F877A
  C8 = Ceramic Capacitor [package=THT]
  D6 = Rectifier Diode
  D9 = Rectifier Diode
  C1 = Ceramic Capacitor [package=THT]
  IC1 = ULN2803A [package=THT]
  U1 = MAX232try2
  D8 = Rectifier Diode
  R23 = 4.7k Ω Resistor [package=THT]
  D13 = Rectifier Diode
  R29 = 4.7k Ω Resistor [package=THT]
  R30 = 4.7k Ω Resistor [package=THT]
  R31 = 1k Ω Resistor [package=THT]

nets:
  N1: R25.Pin_0, R18.Pin_0, R26.Pin_0, R24.Pin_0, R19.Pin_0, Componente1.connector20, R28.Pin_0, R17.Pin_0, R22.Pin_0, R20.Pin_0, R21.Pin_0, R27.Pin_0, Power_plug2.VCC, Componente2.connector14, R14.Pin_0, R16.Pin_1, PIC_16F877A1.connector10, C1.pin_1, R23.Pin_0
  N2: R25.Pin_1, D12.connector1, PIC_16F877A1.connector16
  N3: D2.connector0, Componente1.connector13
  N4: D2.connector1, R18.Pin_1, PIC_16F877A1.connector2
  GND: C10.pin_0, Power_plug1.GND, Componente1.connector21, Componente1.connector22, Componente1.connector23, Componente1.connector24, S1.leg1, U2.Pin_4, C11.pin_1, S3.COM, C2.-, Power_plug2.GND, Componente2.connector15, Componente2.connector16, Componente2.connector17, Componente2.connector18, S2.COM, C7.pin_1, C5.+, IC2.0V, PIC_16F877A1.connector11, PIC_16F877A1.connector30, C8.pin_1, C1.pin_0, IC1.0V, U1.connector14
  N5: C10.pin_1, XTAL1.pin_1, PIC_16F877A1.connector12
  N6: D7.connector0, Componente1.connector5
  N7: D7.connector1, PIC_16F877A1.connector14, R23.Pin_1
  N8: D3.connector0, Componente1.connector1
  N9: D3.connector1, R19.Pin_1, PIC_16F877A1.connector3
  N10: R26.Pin_1, PIC_16F877A1.connector17, D9.connector1
  N11: C6.-, U1.connector4
  N12: C6.+, U1.connector3
  N13: D5.connector0, Componente1.connector3
  N14: D5.connector1, R21.Pin_1, PIC_16F877A1.connector5
  N15: R24.Pin_1, D11.connector1, PIC_16F877A1.connector15
  N16: Power_plug1.VCC, Componente2.connector19, Componente2.connector20, Componente2.connector21, IC2.COM_-_Common, IC1.COM_-_Common
  N17: Componente1.connector0, D1.connector0
  N18: Componente1.connector2, D4.connector0
  N19: Componente1.connector4, D6.connector0
  N20: Componente1.connector6, Componente2.connector0, D11.connector0
  N21: Componente1.connector7, D12.connector0, Componente2.connector1
  N22: Componente1.connector8, Componente2.connector2, D9.connector0
  N23: Componente1.connector9, Componente2.connector3, D8.connector0
  N24: Componente1.connector10, D10.connector0, Componente2.connector4
  N25: Componente1.connector11, Componente2.connector5, IC1.Out_1
  N26: Componente1.connector12, Componente2.connector6, IC1.Out_2
  N27: Componente1.connector14, U2.Pin_2
  N28: Componente1.connector15, Componente1.connector16, U1.connector7
  N29: Componente1.connector17, U1.connector6
  N30: Componente1.connector18, IC2.Out_2
  N31: R28.Pin_1, D10.connector1, PIC_16F877A1.connector23
  N32: R17.Pin_1, D1.connector1, PIC_16F877A1.connector1
  N33: R22.Pin_1, PIC_16F877A1.connector6, D6.connector1
  N34: C9.pin_0, PIC_16F877A1.connector31, U1.connector15, R29.Pin_1, R30.Pin_1
  N35: C9.pin_1, U1.connector1
  N36: R20.Pin_1, D4.connector1, PIC_16F877A1.connector4
  N37: S1.leg0, PIC_16F877A1.connector0, D13.connector0
  N38: U2.Pin_1, R16.Pin_0
  N39: U2.Pin_5, R14.Pin_1, C7.pin_0, PIC_16F877A1.connector32, C8.pin_0
  N40: C4.-, U1.connector0
  N41: C4.+, U1.connector2
  N42: R27.Pin_1, PIC_16F877A1.connector22, D8.connector1
  N43: C11.pin_0, XTAL1.pin_0, PIC_16F877A1.connector13
  N44: S3.L1, PIC_16F877A1.connector26
  N45: Componente2.connector7, IC1.Out_3
  N46: Componente2.connector8, IC1.Out_4
  N47: Componente2.connector9, IC1.Out_5
  N48: Componente2.connector10, IC1.Out_6
  N49: Componente2.connector11, IC1.Out_7
  N50: Componente2.connector12, IC1.Out_8
  N51: Componente2.connector22, IC2.Out_4
  N52: Componente2.connector23, IC2.Out_3
  N53: Componente2.connector24, IC2.Out_1
  N54: S2.L1, PIC_16F877A1.connector27, R29.Pin_0, R30.Pin_0, R31.Pin_1
  N55: C5.-, U1.connector5
  N56: IC2.In_1, PIC_16F877A1.connector19
  N57: IC2.In_3, PIC_16F877A1.connector9
  N58: IC2.In_4, PIC_16F877A1.connector21
  N59: PIC_16F877A1.connector18, IC1.In_1
  N60: PIC_16F877A1.connector33, IC1.In_8
  N61: PIC_16F877A1.connector34, IC1.In_7
  N62: PIC_16F877A1.connector35, IC1.In_6
  N63: PIC_16F877A1.connector36, IC1.In_5
  N64: PIC_16F877A1.connector37, IC1.In_4
  N65: PIC_16F877A1.connector38, IC1.In_3
  N66: PIC_16F877A1.connector39, IC1.In_2
