# Fritzing sketch id3057_PlantBreedingDevice_0 (saved by Fritzing 0.9.0b)
breadboards: 1

parts:
  パーツ1 = Arduino Mega ADK (Rev3)
  R1 = Resistor [tolerance=±5% resistance=220 package=THT]
  R2 = Resistor [tolerance=±5% resistance=220 package=THT]
  R3 = Resistor [tolerance=±5% resistance=220 package=THT]
  R4 = Resistor [tolerance=±5% resistance=220 package=THT]
  R5 = Resistor [tolerance=±5% resistance=220 package=THT]
  R6 = Resistor [tolerance=±5% resistance=220 package=THT]
  R7 = Resistor [tolerance=±5% resistance=220 package=THT]
  R8 = Resistor [tolerance=±5% resistance=220 package=THT]
  R9 = Resistor [tolerance=±5% resistance=220 package=THT]
  LED1 = Super Flux RGB LED (com. cathode)
  LED2 = Super Flux RGB LED (com. cathode)
  LED3 = Super Flux RGB LED (com. cathode)
  J1 = Peltier Element
  J2 = Peltier Element
  Q1 = MOSFET-NCHANNEL [package=to220v]
  Q2 = MOSFET-NCHANNEL [package=to220v]
  R10 = Resistor [tolerance=±5% resistance=220 package=THT]
  R11 = Resistor [tolerance=±5% resistance=220 package=THT]
  R12 = Resistor [tolerance=±5% resistance=220 package=THT]
  Q3 = MOSFET-NCHANNEL [package=to220v]
  M1 = DC Motor
  AM2303 = Humidity and Temperature Sensor RHT03
  R13 = Resistor [tolerance=±5% resistance=220 package=THT]

nets:
  N1: パーツ1.D13_PWM, R12.Pin_0, Q3.G
  N2: パーツ1.D12_PWM, Q2.G, R11.Pin_0
  N3: パーツ1.D11_PWM, Q1.G, R10.Pin_0
  N4: パーツ1.D10_PWM, R9.Pin_1
  N5: パーツ1.D9_PWM, R8.Pin_1
  N6: パーツ1.D8_PWM, R7.Pin_1
  5V: パーツ1.5V, LED1.common_cathode, LED2.common_cathode, LED3.common_cathode, AM2303.Vcc, R13.Pin_1
  N7: パーツ1.GND, Q1.S, Q2.S, R10.Pin_1, R11.Pin_1, R12.Pin_1, Q3.S, AM2303.GND_1, AM2303.GND_2
  N8: パーツ1.D2_PWM, R1.Pin_1
  N9: パーツ1.D3_PWM, R2.Pin_1
  N10: パーツ1.D4_PWM, R3.Pin_1
  N11: パーツ1.D5_PWM, R4.Pin_1
  N12: パーツ1.D6_PWM, R5.Pin_1
  N13: パーツ1.D7_PWM, R6.Pin_1
  N14: パーツ1.D22, AM2303.Data-signal, R13.Pin_0
  N15: R1.Pin_0, LED1.red_anode
  N16: R2.Pin_0, LED1.green_anode
  N17: R3.Pin_0, LED1.blue_anode
  N18: R4.Pin_0, LED2.red_anode
  N19: R5.Pin_0, LED2.green_anode
  N20: R6.Pin_0, LED2.blue_anode
  N21: R7.Pin_0, LED3.red_anode
  N22: R8.Pin_0, LED3.green_anode
  N23: R9.Pin_0, LED3.blue_anode
  N24: J1.pin1, Q2.D
  N25: J1.pin2, J2.pin2, M1.pin_1
  N26: J2.pin1, Q1.D
  N27: Q3.D, M1.pin_2

notes:
  TEC1-12704
  ( Heat ) ( Cool )
  2SK358
  (N-channel mosfet)
  Fan Motor
  外部電源へ
  (6〜12V ?)
  http://bit.ly/1tClYnE
  を参考にDHT配線変更（20141110)
  4.7k抵抗を介して5Vと接続
