# Fritzing sketch id3058_plant_0 (saved by Fritzing 0.9.3b)

parts:
  RHT1 = Humidity and Temperature Sensor RHT03
  Part1 = Soil Moisture Sensor
  U1 = ESP8266 WiFi Module [part_number=ESP8266]
  Part2 = Arduino Mega 2560 (Rev3)
  T1 = LM35 Temperature Sensor [package="TO92 [THT]"]
  R1 = Resistor [tolerance=±5% resistance=1k package=THT]
  Part3 = Logic Level Converter

nets:
  VCC: RHT1.Vcc, Part1.VCC, Part2.5V, T1.+Vs, R1.Pin_0, Part3.HV
  N1: RHT1.Data-signal, Part2.A2, R1.Pin_1
  GND: RHT1.GND_2, Part1.GND, U1.GND, U1.GPIO_15, Part2.GND, T1.GND
  N2: Part1.SIG, Part2.A0
  N3: U1.RXD, Part3.TX2_LV
  VCC_2: U1.VCC, U1.CH_PD, U1.REST, Part2.3V3, Part3.LV
  N4: U1.TXD, Part3.RX2_HV
  N5: Part2.A1, T1.Vout
  N6: Part2.D15/RX3, Part3.TX_LV
  N7: Part2.D14/TX3, Part3.RX_HV
