# Fritzing sketch id3059_wateringsensor_0 (saved by Fritzing 0.9.3b)
circuit board: 2.86041cm x 15.8819cm
breadboards: 1

parts:
  U1 = attiny85 [package=dip]
  R1 = Resistor [tolerance=±5% resistance=220 package=THT]
  BAT5 = Battery Holders [package=battcom_20mm_pth]
  SG3 = Buzzer 12mm [package=buzzer-12mm-ns-kit]
  LED1 = LED - 3mm [color="Red (633nm)" package="3 mm [THT]"]
  R2 = Resistor [tolerance=±5% resistance=220 package=THT]
  S1 = SWITCH-MOMENTARY-2 [package=tactile-pth]
  J2 = female pin header, 8 pins [form="♀ (female)"]
  Pad2 = Pad [width=9.9900000000000002 height=102.78071525566881 connect=center]
  Pad1 = Pad [width=9.9909112692009749 height=102.78071525566887 connect=center]

nets:
  N1: U1.Pin_1, S1.2, J2.pin1
  N2: U1.Pin_2, J2.pin3
  N3: U1.Pin_3, J2.pin2
  N4: U1.Pin_4, BAT5.-, SG3.2, LED1.cathode, S1.1, J2.pin8, Pad1.pad
  N5: U1.Pin_5, SG3.1, J2.pin6
  N6: U1.Pin_6, R2.Pin_0, J2.pin5
  N7: U1.Pin_7, R1.Pin_1, J2.pin4, Pad2.pad
  N8: U1.Pin_8, R1.Pin_0, BAT5.+, J2.pin7
  N9: LED1.anode, R2.Pin_1

notes:
  4
  3
  2
  1
  0
  vcc
  gnd
  rst
