# Fritzing sketch id3062_7segemnt_0 (saved by Fritzing 0.7.4b)
breadboards: 1

parts:
  Arduino1 = Arduino
  7_Segment1 = 7 Segment Display

nets:
  N1: Arduino1.GND, 7_Segment1.common_anode
  N2: Arduino1.D13, 7_Segment1.Segment_A
  N3: Arduino1.D12, 7_Segment1.Segment_B
  N4: Arduino1.D11, 7_Segment1.Segment_C
  N5: Arduino1.D10, 7_Segment1.Segment_D
  N6: Arduino1.D9, 7_Segment1.Segment_E
  N7: Arduino1.D8, 7_Segment1.Segment_F
  N8: Arduino1.D7, 7_Segment1.Segment_G
  N9: Arduino1.D6, 7_Segment1.Segment_DP

notes:
  blue = ''a'' segment - pin 13
  red = "b" segment - pin 12
  yellow = ''c'' segment - pin 11
  green = ''d'' segement - pin 10
  grey = ''e'"egment - pin 9
  orange = "f' segment - pin 8
  brown = ''g'' segment - pin 7
  purple = ''DP'' - pin 6
