# Fritzing sketch id3063_Diara_play_pause_keyboard_0 (saved by Fritzing 0.9.3b)

parts:
  Componente1 = Arduino Leonardo (Rev3b)
  S1 = Square Pushbutton
  JACK1 = 2.1mm_Barrel_Jack_with_Terminal_Block

nets:
  N1: Componente1.D4/A6, JACK1.connector1
  N2: Componente1.D7, S1.leg1
  N3: Componente1.GND, S1.leg0, JACK1.connector2
