# Fritzing sketch id3064_PlaymoDrone_0 (saved by Fritzing 0.9.2b)
circuit board: 8.46667cm x 5.64444cm
breadboards: 1

parts:
  PlaymoDrone = Arduino Uno (Rev3) - ICSP
  L293D = L293D [package=THT]
  Moteur = DC Motor
  VCC1_9V = Battery block 9V
  C1 = Electrolytic Capacitor [capacitance=100µF package="200 mil [THT, electrolytic]"]
  Part2 = Bluetooth HC-05 Macho
  LED3 = LED - 5mm [color="Blue (470nm)" package="5 mm [THT]"]
  Servo = Basic Servo
  LED7 = LED - 5mm [color="Green (555nm)" package="5 mm [THT]"]
  LED8 = LED - 5mm [color="Red (660nm)" package="5 mm [THT]"]
  LED9 = LED - 5mm [color="White (4500K)" package="5 mm [THT]"]
  Photo2 = PHOTOCELL [package=photocell]
  photo1 = PHOTOCELL [package=photocell]
  R6 = Resistor [tolerance=±5% resistance=220 package=THT]
  R7 = Resistor [tolerance=±5% resistance=220 package=THT]
  R8 = Resistor [tolerance=±5% resistance=220 package=THT]
  R9 = Resistor [tolerance=±5% resistance=220 package=THT]
  HC-SR04 = SRF05 Ultrasonic Rangefinder

nets:
  N1: PlaymoDrone.A0, Photo2.P$1
  N2: PlaymoDrone.A1, photo1.P$1
  VCC: PlaymoDrone.5V, L293D.+V, Part2.VCC, Servo.vcc, HC-SR04.connector8
  GND: PlaymoDrone.GND, L293D.0V, VCC1_9V.-, C1.-, Part2.Key, Part2.GND, Servo.gnd, Photo2.P$2, photo1.P$2, R6.Pin_1, R7.Pin_0, R8.Pin_0, R9.Pin_1, HC-SR04.connector11
  N3: PlaymoDrone.D8, L293D.In_4, LED8.anode
  N4: PlaymoDrone.D10_PWM/SS, Part2.TXD
  N5: PlaymoDrone.D11_PWM/MOSI, Part2.RXD
  N6: PlaymoDrone.D12/MISO, LED9.anode
  N7: PlaymoDrone.D13/SCK, Servo.pulse
  N8: PlaymoDrone.D2, HC-SR04.connector10
  N9: PlaymoDrone.D4, HC-SR04.connector9
  N10: PlaymoDrone.D6_PWM, L293D.Enable_2
  N11: PlaymoDrone.D7, L293D.In_3, LED7.anode
  N12: L293D.+Vmotor, VCC1_9V.+, C1.+
  N13: L293D.Out_3_(_Controlled_by_Enable_2_), Moteur.pin_2
  N14: L293D.Out_4_(_Controlled_by_Enable_2_), Moteur.pin_1
  N15: Part2.State, LED3.anode
  N16: LED3.cathode, R9.Pin_0
  N17: LED7.cathode, R8.Pin_1
  N18: LED8.cathode, R7.Pin_1
  N19: LED9.cathode, R6.Pin_0
