# Fritzing sketch id3065_PLC_display_serial_monitor_0 (saved by Fritzing 0.9.0b)
circuit board: 6.88566cm x 5.36311cm
breadboards: 2

parts:
  R2 = Resistor [tolerance=±5% resistance=220 package=THT]
  Contrast1 = Rotary Potentiometer (Small) [maximum_resistance=100kΩ package=THT]
  Arduino1 = Arduino Uno (Rev3)
  R3 = Resistor [tolerance=±5% resistance=10k package=THT]
  R4 = Resistor [tolerance=±5% resistance=10k package=THT]
  R5 = Resistor [tolerance=±5% resistance=10k package=THT]
  Peso_1 = Pushbutton [package="[THT]"]
  Peso_2 = Pushbutton [package="[THT]"]
  Peso_4 = Pushbutton [package="[THT]"]
  LCD1 = LCD screen

nets:
  N1: R2.Pin_0, LCD1.LED+
  5V: R2.Pin_1, Contrast1.leg2, Arduino1.5V, Peso_1.Pin_3, Peso_1.Pin_4, Peso_2.Pin_3, Peso_2.Pin_4, Peso_4.Pin_3, Peso_4.Pin_4, LCD1.VDD
  GND: Contrast1.leg1, Arduino1.GND, R3.Pin_1, R4.Pin_1, R5.Pin_1, LCD1.VSS, LCD1.R/W, LCD1.LED-
  N2: Contrast1.wiper, LCD1.V0
  N3: Arduino1.D8, R4.Pin_0, Peso_2.Pin_1, Peso_2.Pin_2
  N4: Arduino1.D9_PWM, R5.Pin_0, Peso_4.Pin_1, Peso_4.Pin_2
  N5: Arduino1.D11_PWM/MOSI, LCD1.E
  N6: Arduino1.D12/MISO, LCD1.RS
  N7: Arduino1.D2, LCD1.DB7
  N8: Arduino1.D3_PWM, LCD1.DB6
  N9: Arduino1.D4, LCD1.DB5
  N10: Arduino1.D5_PWM, LCD1.DB4
  N11: Arduino1.D7, R3.Pin_0, Peso_1.Pin_1, Peso_1.Pin_2

notes:
  Uscite PLC
