# Fritzing sketch id3066_PlotMath_Esquema_0 (saved by Fritzing 0.9.2b)
breadboards: 1

parts:
  Componente1 = Arduino Uno (Rev3)
  LED1 = LED - 5mm [color="Green (565nm)" package="5 mm [THT]"]
  Esquerda-3 = Basic Servo
  Direita-4 = Basic Servo
  Elevador-1 = Basic Servo
  Bluetooth = Bluetooth Module Breakout - Roving Networks (RN-41)
  R2_680 = Resistor [tolerance=±5% resistance=680 package="2512 [SMD]"]
  R1_470 = Resistor [tolerance=±5% resistance=470 package=THT]
  R1 = Resistor [tolerance=±5% resistance=220 package=THT]
  R2 = Resistor [tolerance=±5% resistance=220 package=THT]
  LED4 = LED - 5mm [color="Red (633nm)" package="5 mm [THT]"]
  LED5 = LED - 5mm [color="Blue (430nm)" package="5 mm [THT]"]
  R3 = Resistor [tolerance=±5% resistance=220 package=THT]

nets:
  N1: Componente1.D11_PWM/MOSI, R3.Pin_0
  N2: Componente1.D12/MISO, R2.Pin_0
  N3: Componente1.D13/SCK, R1.Pin_0
  VCC: Componente1.5V, Esquerda-3.vcc, Direita-4.vcc, Elevador-1.vcc, Bluetooth.VCC
  GND: Componente1.GND, LED1.cathode, Direita-4.gnd, Elevador-1.gnd, Bluetooth.GND, LED4.cathode, LED5.cathode
  N4: LED1.anode, R1.Pin_1
  N5: Bluetooth.UARTRX, R1_470.Pin_0
  N6: R2_680.Pin_0, R1_470.Pin_1
  N7: R2.Pin_1, LED5.anode
  N8: LED4.anode, R3.Pin_1
