# Fritzing sketch id3067_L298N_Circuit_0 (saved by Fritzing 0.9.3b)
breadboards: 1

parts:
  Arduino_UNO = Arduino Uno (Rev3)
  VCC1 = Battery
  VCC2 = Battery
  VCC3 = Battery
  L298N = L298_BRIDGE_DRIVER [package=powerso20]
  LED_Cerrado = LED - 5mm [color="Red (633nm)" package="5 mm [THT]"]
  R1 = Resistor [tolerance=±5% resistance=330 package=THT]
  LED_Abierto = LED - 5mm [color="Green (555nm)" package="5 mm [THT]"]
  R1_2 = Resistor [tolerance=±5% resistance=330 package=THT]
  VCC5 = Battery
  LS2 = Momentary Switch [package=ksa_sealed_tac_switch]
  LS1 = Momentary Switch [package=ksa_sealed_tac_switch]
  PB = Momentary Switch [package=ksa_sealed_tac_switch]
  Motor = DC Motor

nets:
  N1: Arduino_UNO.D8, PB.3
  N2: Arduino_UNO.D10_PWM/SS, L298N.ENA
  N3: Arduino_UNO.D12/MISO, LED_Cerrado.anode
  N4: Arduino_UNO.D13/SCK, LED_Abierto.anode
  GND: Arduino_UNO.GND, L298N.GND, R1.Pin_0, R1_2.Pin_0, VCC5.-
  N5: Arduino_UNO.D3_PWM, L298N.IN1
  N6: Arduino_UNO.D5_PWM, L298N.IN2
  N7: Arduino_UNO.D6_PWM, LS1.3
  N8: Arduino_UNO.D7, LS2.3
  N9: Arduino_UNO.5V, LS2.1, LS1.1, PB.1
  VIN: Arduino_UNO.VIN, L298N.VSS
  N10: VCC1.-, VCC2.+
  N11: VCC1.+, L298N.VS
  N12: VCC2.-, VCC3.+
  N13: VCC3.-, VCC5.+
  N14: L298N.OUT1, Motor.pin_2
  N15: L298N.OUT2, Motor.pin_1
  N16: LED_Cerrado.cathode, R1_2.Pin_1
  N17: R1.Pin_1, LED_Abierto.cathode
