# Fritzing sketch id3068_plus_minus_testing_board_0 (saved by Fritzing 0.9.3b)
circuit board: 1.71453cm x 0.948305cm

parts:
  J1 = female pin header, 2 pins [form="♀ (female)"]
  LED2 = LEDs [package=led-1206]
  J3 = female pin header, 2 pins [form="♀ (female)"]
  J2 = female pin header, 2 pins [form="♀ (female)"]

nets:
  N1: J1.pin1, J3.pin1
  N2: J1.pin2, LED2.A, J2.pin2
  N3: LED2.C, J3.pin2, J2.pin1

notes:
  plus-minus testing board
  output
  LED
  input
  5v
  GND
