# Fritzing sketch id3069_Pn532_PI_0 (saved by Fritzing 0.9.2b)
breadboards: 1

parts:
  R1 = Resistor [tolerance=±5% resistance=220 package=THT]
  R2 = Resistor [tolerance=±5% resistance=220 package=THT]
  R3 = Resistor [tolerance=±5% resistance=220 package=THT]
  R4 = Resistor [tolerance=±5% resistance=220 package=THT]
  R5 = Resistor [tolerance=±5% resistance=220 package=THT]
  R6 = Resistor [tolerance=±5% resistance=220 package=THT]
  Raspberry_Pi1 = Raspberry Pi B rev2

nets:
  N1: R1.Pin_0, R4.Pin_0, Raspberry_Pi1.GND
  N2: R1.Pin_1, R2.Pin_0
  N3: R2.Pin_1, R3.Pin_0, Raspberry_Pi1.GPIO_14
  N4: R4.Pin_1, R5.Pin_0
  N5: R5.Pin_1, R6.Pin_0, Raspberry_Pi1.GPIO_15

notes:
  To PN532 SCL
  To PN532 SDA
