# Fritzing sketch id306_tr_switch_v1_1_0 (saved by Fritzing 0.8.7b)
circuit board: 4.2cm x 5.64444cm
breadboards: 1

parts:
  J1 = Screw terminal - 2 pins [package=THT]
  J2 = Screw terminal - 2 pins [package=THT]
  J3 = Screw terminal - 2 pins [package=THT]
  J4 = Screw terminal - 2 pins [package=THT]
  J5 = Screw terminal - 2 pins [package=THT]
  IC1 = IC, DIP package, 4 pins [chip_label=IC]
  J6 = Screw terminal - 2 pins [package=THT]
  U1 = Transformer [package=transformer]
  U2 = Transformer [package=transformer]
  LED1 = LED - 5mm [color="Red (633nm)" package="5 mm [THT]"]
  LED2 = LED - 5mm [color="Green (560nm)" package="5 mm [THT]"]
  R1 = Resistor [tolerance=±5% resistance=220 package=THT]
  R2 = Resistor [tolerance=±5% resistance=100 package=THT]

nets:
  N1: J1.pin1, U2.4
  N2: J1.pin2, U2.3
  N3: J2.pin1, U1.4
  N4: J2.pin2, U1.3
  N5: J3.pin1, U1.1
  N6: J3.pin2, U1.2
  N7: J4.pin1, U2.1
  N8: J4.pin2, U2.2
  N9: J5.pin1, R2.Pin_0
  N10: J5.pin2, IC1.pin2, LED1.anode
  N11: IC1.pin1, LED2.cathode
  N12: IC1.pin3, J6.pin2
  N13: J6.pin1, R1.Pin_1
  N14: LED1.cathode, LED2.anode, R2.Pin_1

notes:
  T/R switch
  v1.1
  R&D by VE2HKW
