# Fritzing sketch id3072_Jacob_Police_0 (saved by Fritzing 0.7.12b)
breadboards: 1

parts:
  Arduino1 = Arduino
  J1 = Piezo Speaker
  LED1 = LED - 5mm [color="Red (633nm)" package="5 mm [THT]"]
  LED2 = LED - 5mm [color="Red (633nm)" package="5 mm [THT]"]
  J2 = Piezo Speaker
  S1 = Pushbutton [package="[THT]"]
  Arduino2 = Arduino
  R1 = Resistor [tolerance=±5% resistance=220 package=THT]

nets:
  N1: Arduino1.D11, Arduino1.D6, J1.pin2
  N2: Arduino1.D10, LED1.anode
  N3: Arduino1.D9, LED2.anode
  N4: J1.pin1, LED1.cathode, LED2.cathode, J2.pin1, R1.Pin_0
  N5: J2.pin2, Arduino2.D2
  N6: S1.Pin_1, S1.Pin_2, Arduino2.D1TX, R1.Pin_1
  N7: S1.Pin_3, S1.Pin_4, Arduino2.3V3
