# Fritzing sketch id3073_Police_Siren_0 (saved by Fritzing 0.8.7b)
circuit board: 8.46667cm x 5.64444cm
breadboards: 1

parts:
  IC2 = IC, DIP package, 8 pins [chip_label=555]
  IC3 = IC, DIP package, 8 pins [chip_label=555]
  R1 = Resistor [tolerance=±5% resistance=10k package=THT]
  C1 = Electrolytic Capacitor [capacitance=10µF package="100 mil [THT, electrolytic]"]
  SPKR1 = Loudspeaker
  C2 = Electrolytic Capacitor [capacitance=10µF package="100 mil [THT, electrolytic]"]
  R2 = Resistor [tolerance=±5% resistance=1k package=THT]
  R3 = Resistor [tolerance=±5% resistance=68k package=THT]
  C3 = Ceramic Capacitor [capacitance=100nF package="100 mil [THT, multilayer]"]
  R4 = Resistor [tolerance=±5% resistance=10k package=THT]
  R5 = Resistor [tolerance=±5% resistance=10k package=THT]
  C4 = Ceramic Capacitor [capacitance=100nF package="100 mil [THT, multilayer]"]

nets:
  N1: IC2.pin1, IC3.pin1, C1.+, SPKR1.pin1, SPKR1.pin2, C2.+, C3.1, C4.1
  N2: IC2.pin2, IC2.pin6, C2.-, R3.Pin_1
  N3: IC2.pin3, R1.Pin_0
  N4: IC2.pin4, IC2.pin8, IC3.pin4, IC3.pin8, R2.Pin_0, R4.Pin_0
  N5: IC2.pin5, C3.0
  N6: IC2.pin7, R2.Pin_1, R3.Pin_0
  N7: IC3.pin2, IC3.pin6, R5.Pin_1, C4.0
  N8: IC3.pin3, C1.-
  N9: IC3.pin5, R1.Pin_1
  N10: IC3.pin7, R4.Pin_1, R5.Pin_0
