# Fritzing sketch id3074_Untitled_Sketch_0 (saved by Fritzing 0.9.3b)
breadboards: 2

parts:
  Part1 = Arduino Uno (Rev3)
  LED1 = LED - 5mm [color="Red (633nm)" package="5 mm [THT]"]
  LED2 = LED - 5mm [color="White (6500K)" package="5 mm [THT]"]
  LED3 = LED - 5mm [color="Blue (470nm)" package="5 mm [THT]"]

nets:
  N1: Part1.D2, LED3.anode
  N2: Part1.D3_PWM, LED1.anode
  N3: Part1.D4, LED2.anode
  N4: Part1.GND, LED1.cathode, LED2.cathode, LED3.cathode
