# Fritzing sketch id3077_Arkanoid2UpdatedVersion_0 (saved by Fritzing 0.8.3b)
breadboards: 1

parts:
  Onderdeel1 = Arduino Uno (Rev3)
  S1 = Pushbutton [package="[THT]"]
  R1 = Resistor [tolerance=±5% resistance=10k package=THT]
  S2 = Pushbutton [package="[THT]"]
  R2 = Resistor [tolerance=±5% resistance=10k package=THT]
  LED1 = 8x8_LED_Matrix__red
  J1 = Piezo Speaker  # not connected

nets (from the schematic view):
  N1: Onderdeel1.A4/SDA, LED1.connector3
  N2: Onderdeel1.A5/SCL, LED1.connector4
  N3: Onderdeel1.GND, R1.Pin_1, R2.Pin_0, LED1.connector2
  N4: Onderdeel1.D2, S2.Pin_3, S2.Pin_4
  N5: Onderdeel1.D3_PWM, S1.Pin_3, S1.Pin_4, R1.Pin_0
  N6: Onderdeel1.5V, S1.Pin_1, S1.Pin_2, S2.Pin_1, S2.Pin_2, R2.Pin_1, LED1.connector1
