# Fritzing sketch id3082_Moteur_RTC_0 (saved by Fritzing 0.8.7b)
breadboards: 1

parts:
  VCC1 = Battery block 9V
  Composant1 = Arduino Uno (Rev3) - ICSP
  U1 = STA540 [package=multiwatt15]
  M4 = DC Motor
  Composant2 = Real Time Clock Module - DS1307 RTC Breakout Board

nets:
  GND: VCC1.-, Composant1.GND, U1.P-GND, Composant2.GND
  N1: Composant1.A4/SDA, Composant2.SDA
  N2: Composant1.A5/SCL, Composant2.SCL
  N3: Composant1.D2, U1.IN2
  N4: Composant1.D3_PWM, U1.STBY
  N5: Composant1.D5_PWM, U1.SVR
  5V: Composant1.5V, Composant2.5V
  N6: U1.OUT2, M4.pin_2
  N7: U1.VCC1, M4.pin_1
