# Fritzing sketch id3083_Pot_to_LED_Array_0 (saved by Fritzing 0.9.3b)
breadboards: 2

parts:
  Part1 = Arduino Uno (Rev3)
  IC1 = SHIFT REGISTER [package=dil16]
  U1 = POT [package=trim_pot]
  LED1 = smd LED [color="Red (633nm)" package="1206 [SMD]"]
  LED2 = smd LED [color="Red (633nm)" package="1206 [SMD]"]
  LED3 = smd LED [color="Red (633nm)" package="1206 [SMD]"]
  LED4 = smd LED [color="Red (633nm)" package="1206 [SMD]"]
  LED5 = smd LED [color="Red (633nm)" package="1206 [SMD]"]
  LED6 = smd LED [color="Red (633nm)" package="1206 [SMD]"]
  LED7 = smd LED [color="Red (633nm)" package="1206 [SMD]"]
  LED8 = smd LED [color="Red (633nm)" package="1206 [SMD]"]
  R1 = Resistor [tolerance=±5% resistance=220 package=THT]
  R2 = Resistor [tolerance=±5% resistance=220 package=THT]
  R3 = Resistor [tolerance=±5% resistance=220 package=THT]
  R4 = Resistor [tolerance=±5% resistance=220 package=THT]
  R7 = Resistor [tolerance=±5% resistance=220 package=THT]
  R8 = Resistor [tolerance=±5% resistance=220 package=THT]
  R9 = Resistor [tolerance=±5% resistance=220 package=THT]
  R10 = Resistor [tolerance=±5% resistance=220 package=THT]

nets:
  N1: Part1.A0, U1.E
  N2: Part1.D8, IC1.RCK
  N3: Part1.D11_PWM/MOSI, IC1.SER
  N4: Part1.D12/MISO, IC1.SCK
  5V: Part1.5V, IC1.SCL, IC1.VCC, U1.S
  GND: Part1.GND, IC1.GND, IC1.G, U1.A, R1.Pin_1, R2.Pin_1, R3.Pin_1, R4.Pin_1, R7.Pin_1, R8.Pin_1, R9.Pin_1, R10.Pin_1
  N5: IC1.QB, LED2.anode
  N6: IC1.QC, LED3.anode
  N7: IC1.QD, LED4.anode
  N8: IC1.QE, LED5.anode
  N9: IC1.QF, LED6.anode
  N10: IC1.QG, LED7.anode
  N11: IC1.QH, LED8.anode
  N12: IC1.QA, LED1.anode
  N13: LED1.cathode, R1.Pin_0
  N14: LED2.cathode, R4.Pin_0
  N15: LED3.cathode, R3.Pin_0
  N16: LED4.cathode, R2.Pin_0
  N17: LED5.cathode, R7.Pin_0
  N18: LED6.cathode, R8.Pin_0
  N19: LED7.cathode, R9.Pin_0
  N20: LED8.cathode, R10.Pin_0
