# Fritzing sketch id3084_potansiyometre_0 (saved by Fritzing 0.9.3b)
breadboards: 1

parts:
  Parça1 = Arduino Uno (Rev3)
  LED1 = LED - 5mm [color="Red (633nm)" package="5 mm [THT]"]
  R2 = Rotary Potentiometer (Small) [maximum_resistance=10kΩ package=THT]  # not connected
  R3 = Resistor [tolerance=±5% resistance=220 package=THT]

nets:
  N1: Parça1.D10_PWM/SS, LED1.cathode
  N2: Parça1.GND, R3.Pin_1
  N3: LED1.anode, R3.Pin_0
