# Fritzing sketch id3086_Arduino_Night_Rider (saved by Fritzing 0.6.3b)
breadboards: 1

parts:
  U1 = 74HC595 [package="DIP16 [THT]"]
  U2 = 74HC595 [package="DIP16 [THT]"]
  R1 = Resistor [resistance=220 tolerance=±5% package=THT]
  R1_2 = Resistor [resistance=220 tolerance=±5% package=THT]
  R1_3 = Resistor [resistance=220 tolerance=±5% package=THT]
  R1_4 = Resistor [resistance=220 tolerance=±5% package=THT]
  R1_5 = Resistor [resistance=220 tolerance=±5% package=THT]
  R1_6 = Resistor [resistance=220 tolerance=±5% package=THT]
  R1_7 = Resistor [resistance=220 tolerance=±5% package=THT]
  R1_8 = Resistor [resistance=220 tolerance=±5% package=THT]
  R1_9 = Resistor [resistance=220 tolerance=±5% package=THT]
  R1_10 = Resistor [resistance=220 tolerance=±5% package=THT]
  R1_11 = Resistor [resistance=220 tolerance=±5% package=THT]
  R1_12 = Resistor [resistance=220 tolerance=±5% package=THT]
  R1_13 = Resistor [resistance=220 tolerance=±5% package=THT]
  R1_14 = Resistor [resistance=220 tolerance=±5% package=THT]
  R1_15 = Resistor [resistance=220 tolerance=±5% package=THT]
  R1_16 = Resistor [resistance=220 tolerance=±5% package=THT]
  Arduino1 = Arduino
  LED5 = LED - 5mm [color="Red (633nm)" package="5 mm [THT]"]
  LED1 = LED - 5mm [color="Red (633nm)" package="5 mm [THT]"]
  LED9 = LED - 5mm [color="Red (633nm)" package="5 mm [THT]"]
  LED13 = LED - 5mm [color="Red (633nm)" package="5 mm [THT]"]
  LED4 = LED - 5mm [color="Red (633nm)" package="5 mm [THT]"]
  LED8 = LED - 5mm [color="Red (633nm)" package="5 mm [THT]"]
  LED12 = LED - 5mm [color="Red (633nm)" package="5 mm [THT]"]
  LED16 = LED - 5mm [color="Red (633nm)" package="5 mm [THT]"]
  LED3 = LED - 5mm [color="Red (633nm)" package="5 mm [THT]"]
  LED7 = LED - 5mm [color="Red (633nm)" package="5 mm [THT]"]
  LED11 = LED - 5mm [color="Red (633nm)" package="5 mm [THT]"]
  LED15 = LED - 5mm [color="Red (633nm)" package="5 mm [THT]"]
  LED2 = LED - 5mm [color="Red (633nm)" package="5 mm [THT]"]
  LED6 = LED - 5mm [color="Red (633nm)" package="5 mm [THT]"]
  LED10 = LED - 5mm [color="Red (633nm)" package="5 mm [THT]"]
  LED14 = LED - 5mm [color="Red (633nm)" package="5 mm [THT]"]  # not connected

nets:
  N1: U1.Q1, LED2.anode
  N2: U1.Q2, LED3.anode
  N3: U1.Q3, LED4.anode
  N4: U1.Q4, LED5.anode
  N5: U1.Q5, LED6.anode
  N6: U1.Q6, LED7.anode
  N7: U1.Q7, LED8.anode
  GND: U1.GND, U1.OE, U2.GND, U2.OE, R1.Pin_1, R1_2.Pin_1, R1_3.Pin_1, R1_4.Pin_1, R1_5.Pin_1, Arduino1.GND
  N8: U1.Q7', U2.DS
  VCC: U1.MR, U1.VCC, U2.MR, U2.VCC, Arduino1.+5V
  N9: U1.SH_CP, U2.SH_CP, Arduino1.D12
  N10: U1.ST_CP, U2.ST_CP, Arduino1.D8
  N11: U1.DS, Arduino1.D11
  N12: U1.Q0, LED1.anode
  N13: U2.Q1, LED10.anode
  N14: U2.Q2, LED11.anode
  N15: U2.Q3, LED12.anode
  N16: U2.Q4, LED13.anode
  N17: U2.Q6, LED15.anode
  N18: U2.Q7, LED16.anode
  N19: U2.Q0, LED9.anode
  N20: R1.Pin_0, LED1.cathode
  N21: R1_2.Pin_0, LED2.cathode
  N22: R1_3.Pin_0, LED3.cathode
  N23: R1_4.Pin_0, LED4.cathode
  N24: R1_5.Pin_0, LED5.cathode
  N25: R1_6.Pin_0, LED6.cathode
  N26: R1_6.Pin_1, R1_7.Pin_1, R1_8.Pin_1, R1_9.Pin_1, R1_10.Pin_1, R1_11.Pin_1, R1_12.Pin_1, R1_13.Pin_1, R1_14.Pin_1, R1_15.Pin_1, R1_16.Pin_1
  N27: R1_7.Pin_0, LED7.cathode
  N28: R1_8.Pin_0, LED8.cathode
  N29: R1_9.Pin_0, LED9.cathode
  N30: R1_10.Pin_0, LED10.cathode
  N31: R1_11.Pin_0, LED11.cathode
  N32: R1_12.Pin_0, LED12.cathode
  N33: R1_13.Pin_0, LED13.cathode
  N34: R1_15.Pin_0, LED15.cathode
  N35: R1_16.Pin_0, LED16.cathode
