# Fritzing sketch id3086_potenciometro_+_1_led_0 (saved by Fritzing 0.9.3b)
breadboards: 1

parts:
  Componente2 = Arduino Uno (Rev3)
  R4 = Resistor [tolerance=±5% resistance=220 package=THT]
  LED4 = LED - 5mm [color="Red (635nm)" package="5 mm [THT]"]
  R8 = Slide Potentiometer [maximum_resistance=0.1MΩ]
  R10 = Rotary Potentiometer (Small) [maximum_resistance=10kΩ package=THT]  # not connected

nets:
  N1: Componente2.A2, R8.wiper
  N2: Componente2.D10_PWM/SS, LED4.anode
  N3: Componente2.5V, R8.leg1
  N4: Componente2.GND, R4.Pin_1, R8.leg2
  N5: R4.Pin_0, LED4.cathode

notes:
  LED ROJO -> PIN 10
  TERMINAL CENTRAL POTENCIOMETRO LINEAL 10K
  --> PIN ANALÓGICO A2
  IES SAN ISIDRO
  DPTO. TECNOLOGÍA
  El potenciómetro puede ser como el que está conectado (deslizador) o rotativo (al lado).
  En ambos casos debe ser de 10Kohmios
