# Fritzing sketch id3087_potenciometro_+_3servomotor_+_leds_0 (saved by Fritzing 0.9.3b)
breadboards: 1

parts:
  Componente2 = Arduino Uno (Rev3)
  R1 = Resistor [tolerance=±5% resistance=220 package=THT]
  LED2 = LED - 5mm [color="Green (570nm)" package="5 mm [THT]"]
  LED3 = LED - 5mm [color="Yellow (595nm)" package="5 mm [THT]"]
  R4 = Resistor [tolerance=±5% resistance=220 package=THT]
  R5 = Resistor [tolerance=±5% resistance=220 package=THT]
  LED4 = LED - 5mm [color="Red (635nm)" package="5 mm [THT]"]
  R8 = Slide Potentiometer [maximum_resistance=0.1MΩ]
  R10 = Rotary Potentiometer (Small) [maximum_resistance=10kΩ package=THT]  # not connected
  J1 = Basic Servo

nets:
  N1: Componente2.A2, R8.wiper
  N2: Componente2.D8, J1.pulse
  N3: Componente2.D10_PWM/SS, LED4.anode
  N4: Componente2.D11_PWM/MOSI, LED3.anode
  N5: Componente2.D12/MISO, LED2.anode
  5V: Componente2.5V, R8.leg1, J1.vcc
  GND: Componente2.GND, R1.Pin_1, R4.Pin_1, R5.Pin_1, R8.leg2, J1.gnd
  N6: R1.Pin_0, LED2.cathode
  N7: LED3.cathode, R5.Pin_0
  N8: R4.Pin_0, LED4.cathode

notes:
  LED VERDE -> PIN 12
  LED AMBAR -> PIN 11
  LED ROJO -> PIN 10
  TERMINAL CENTRAL POTENCIOMETRO LINEAL 10K
  --> PIN ANALÓGICO A2
  IES SAN ISIDRO
  DPTO. TECNOLOGÍA
  CONTROL SERVOMOTOR
  PIN --> DIGITAL 8
