# Fritzing sketch id3088_brilloLED_potenciometro_ConSumbador_0 (saved by Fritzing 0.9.2b)
breadboards: 1

parts:
  Parte1 = Arduino Uno (Rev3)
  LED1 = LED - 5mm [color="Red (633nm)" package="5 mm [THT]"]
  R1 = Rotary Potentiometer (Small) [maximum_resistance=100kΩ package=THT]
  R2 = Resistor [tolerance=±5% resistance=220 package=THT]
  J1 = Piezo Speaker

nets:
  N1: Parte1.A0, R1.wiper
  N2: Parte1.D9_PWM, LED1.anode, J1.pin2
  N3: Parte1.GND, R1.leg2, R2.Pin_1, J1.pin1
  N4: Parte1.5V, R1.leg1
  N5: LED1.cathode, R2.Pin_0
