# Fritzing sketch id3089_potentio_led_fritzing_0 (saved by Fritzing 0.9.3b)
breadboards: 1

parts:
  R1 = Rotary Potentiometer (Small) [maximum_resistance=100kΩ package=THT]
  부품1 = Arduino Uno (Rev3)
  LED1 = LED - 5mm [color="Red (633nm)" package="5 mm [THT]"]
  R2 = Resistor [tolerance=±5% resistance=220 package=THT]

nets:
  N1: R1.leg1, 부품1.5V
  N2: R1.wiper, 부품1.A0
  N3: R1.leg2, 부품1.GND, R2.Pin_0
  N4: 부품1.D3_PWM, LED1.anode
  N5: LED1.cathode, R2.Pin_1
