# Fritzing sketch id308_ALM01_FROSH_0 (saved by Fritzing 0.8.0b)
breadboards: 1

parts:
  Parte1 = Arduino Uno (Rev3)  # not connected
  Parte2 = Ambient Light Sensor (TEMT6000 Breakout Board)
  Parte3 = Arduino MicroSD Shield
  VCC1 = Battery block 9V
  S1 = Toggle Switch [package=THT]

nets:
  VCC: Parte2.VCC, Parte3.5V
  GND: Parte2.GND, Parte3.GND
  N1: Parte2.S, Parte3.A0
  N2: VCC1.+, S1.COM
