# Fritzing sketch id3091_AnalogReadSerial_fritzing_0 (saved by Fritzing 0.9.3b)
breadboards: 1

parts:
  R1 = Rotary Potentiometer (Small) [maximum_resistance=100kΩ package=THT]
  부품1 = Arduino Uno (Rev3)

nets:
  N1: R1.leg1, 부품1.5V
  N2: R1.wiper, 부품1.A0
  N3: R1.leg2, 부품1.GND
