# Fritzing sketch id3092_POTLED_0 (saved by Fritzing 0.9.2b)
breadboards: 2

parts:
  Part1 = Arduino Uno (Rev3)
  R1 = Rotary Potentiometer (Small) [maximum_resistance=100kΩ package=THT]
  U1 = 74HC595 SMD [package="SO16 [SMD]"]
  R2 = Resistor [tolerance=±5% resistance=220 package=THT]
  R3 = Resistor [tolerance=±5% resistance=220 package=THT]
  R4 = Resistor [tolerance=±5% resistance=220 package=THT]
  R5 = Resistor [tolerance=±5% resistance=220 package=THT]
  R6 = Resistor [tolerance=±5% resistance=220 package=THT]
  R7 = Resistor [tolerance=±5% resistance=220 package=THT]
  R8 = Resistor [tolerance=±5% resistance=220 package=THT]
  R9 = Resistor [tolerance=±5% resistance=220 package=THT]
  LED1 = LED - 3mm [color="Red (633nm)" package="3 mm [THT]"]
  LED2 = LED - 3mm [color="Red (633nm)" package="3 mm [THT]"]
  LED3 = LED - 3mm [color="Red (633nm)" package="3 mm [THT]"]
  LED4 = LED - 3mm [color="Red (633nm)" package="3 mm [THT]"]
  LED5 = LED - 3mm [color="Red (633nm)" package="3 mm [THT]"]
  LED6 = LED - 3mm [color="Red (633nm)" package="3 mm [THT]"]
  LED7 = LED - 3mm [color="Red (633nm)" package="3 mm [THT]"]
  LED8 = LED - 3mm [color="Red (633nm)" package="3 mm [THT]"]

nets:
  N1: Part1.A2, R1.wiper
  N2: Part1.D8, U1.ST_CP
  N3: Part1.D11_PWM/MOSI, U1.DS
  N4: Part1.D12/MISO, U1.SH_CP
  5V: Part1.5V, R1.leg2, U1.MR, U1.VCC
  GND: Part1.GND, R1.leg1, U1.GND, U1.OE, LED1.cathode, LED2.cathode, LED3.cathode, LED4.cathode, LED5.cathode, LED6.cathode, LED7.cathode, LED8.cathode
  N5: U1.Q1, R3.Pin_0
  N6: U1.Q2, R4.Pin_0
  N7: U1.Q3, R5.Pin_0
  N8: U1.Q4, R8.Pin_0
  N9: U1.Q5, R7.Pin_0
  N10: U1.Q6, R6.Pin_0
  N11: U1.Q7, R9.Pin_0
  N12: U1.Q0, R2.Pin_0
  N13: R2.Pin_1, LED1.anode
  N14: R3.Pin_1, LED2.anode
  N15: R4.Pin_1, LED3.anode
  N16: R5.Pin_1, LED4.anode
  N17: R6.Pin_1, LED5.anode
  N18: R7.Pin_1, LED7.anode
  N19: R8.Pin_1, LED6.anode
  N20: R9.Pin_1, LED8.anode
