# Fritzing sketch id3093_potentiometer_0 (saved by Fritzing 0.8.7b)
breadboards: 1

parts:
  Part1 = Arduino Uno (Rev3)
  R1 = Trimmer Potentiometer [maximum_resistance=10kΩ package=THT]
  R2 = Resistor [tolerance=±5% resistance=220 package=THT]
  LED1 = LED - 5mm [color="Red (633nm)" package="5 mm [THT]"]

nets:
  N1: Part1.A0, R1.wiper
  N2: Part1.D9_PWM, R2.Pin_0
  N3: Part1.GND, R1.leg2, LED1.anode
  N4: Part1.5V, R1.leg1
  N5: R2.Pin_1, LED1.cathode
