# Fritzing sketch id3096_POV_THT_final_0 (saved by Fritzing 0.7.0b)
breadboards: 1

parts:
  IC1 = IC, DIP package, 8 pins [chip_label=IC spacing=300mil]
  R1 = Resistor [tolerance=±5% resistance=220 package=THT]
  R2 = Resistor [tolerance=±5% resistance=220 package=THT]
  R4 = Resistor [tolerance=±5% resistance=220 package=THT]
  LED1 = LED - 3mm [color="Red (633nm)" package="3 mm [THT]"]
  LED2 = LED - 3mm [color="Red (633nm)" package="3 mm [THT]"]
  LED4 = LED - 3mm [color="Red (633nm)" package="3 mm [THT]"]
  LED3 = LED - 3mm [color="Red (633nm)" package="3 mm [THT]"]
  IC2 = IC, DIP package, 8 pins [chip_label=IC spacing=300mil]
  R5 = Resistor [tolerance=±5% resistance=220 package=THT]
  R6 = Resistor [tolerance=±5% resistance=220 package=THT]
  R7 = Resistor [tolerance=±5% resistance=220 package=THT]
  R8 = Resistor [tolerance=±5% resistance=220 package=THT]
  LED5 = LED - 3mm [color="Red (633nm)" package="3 mm [THT]"]
  LED6 = LED - 3mm [color="Red (633nm)" package="3 mm [THT]"]
  LED7 = LED - 3mm [color="Red (633nm)" package="3 mm [THT]"]
  LED8 = LED - 3mm [color="Red (633nm)" package="3 mm [THT]"]
  R3 = Resistor [tolerance=±5% resistance=220 package=THT]
  IC3 = IC, DIP package, 8 pins [chip_label=IC spacing=300mil]
  IC4 = IC, DIP package, 8 pins [chip_label=IC spacing=300mil]
  R9 = Resistor [tolerance=±5% resistance=220 package=THT]
  R10 = Resistor [tolerance=±5% resistance=220 package=THT]
  R11 = Resistor [tolerance=±5% resistance=220 package=THT]
  R12 = Resistor [tolerance=±5% resistance=220 package=THT]
  R13 = Resistor [tolerance=±5% resistance=220 package=THT]
  R14 = Resistor [tolerance=±5% resistance=220 package=THT]
  R15 = Resistor [tolerance=±5% resistance=220 package=THT]
  R16 = Resistor [tolerance=±5% resistance=220 package=THT]
  LED9 = LED - 3mm [color="Red (633nm)" package="3 mm [THT]"]
  LED10 = LED - 3mm [color="Red (633nm)" package="3 mm [THT]"]
  LED11 = LED - 3mm [color="Red (633nm)" package="3 mm [THT]"]
  LED12 = LED - 3mm [color="Red (633nm)" package="3 mm [THT]"]
  LED13 = LED - 3mm [color="Red (633nm)" package="3 mm [THT]"]
  LED14 = LED - 3mm [color="Red (633nm)" package="3 mm [THT]"]
  LED15 = LED - 3mm [color="Red (633nm)" package="3 mm [THT]"]
  LED16 = LED - 3mm [color="Red (633nm)" package="3 mm [THT]"]
  IC5 = IC, DIP package, 8 pins [chip_label=IC spacing=300mil]
  IC6 = IC, DIP package, 8 pins [chip_label=IC spacing=300mil]
  IC7 = IC, DIP package, 8 pins [chip_label=IC spacing=300mil]
  IC8 = IC, DIP package, 8 pins [chip_label=IC spacing=300mil]
  R17 = Resistor [tolerance=±5% resistance=220 package=THT]
  R18 = Resistor [tolerance=±5% resistance=220 package=THT]
  R19 = Resistor [tolerance=±5% resistance=220 package=THT]
  R21 = Resistor [tolerance=±5% resistance=220 package=THT]
  R22 = Resistor [tolerance=±5% resistance=220 package=THT]
  R23 = Resistor [tolerance=±5% resistance=220 package=THT]
  R24 = Resistor [tolerance=±5% resistance=220 package=THT]
  R25 = Resistor [tolerance=±5% resistance=220 package=THT]
  R26 = Resistor [tolerance=±5% resistance=220 package=THT]
  R27 = Resistor [tolerance=±5% resistance=220 package=THT]
  R28 = Resistor [tolerance=±5% resistance=220 package=THT]
  R29 = Resistor [tolerance=±5% resistance=220 package=THT]
  R30 = Resistor [tolerance=±5% resistance=220 package=THT]
  R31 = Resistor [tolerance=±5% resistance=220 package=THT]
  R32 = Resistor [tolerance=±5% resistance=220 package=THT]
  LED17 = LED - 3mm [color="Red (633nm)" package="3 mm [THT]"]
  LED18 = LED - 3mm [color="Red (633nm)" package="3 mm [THT]"]
  LED19 = LED - 3mm [color="Red (633nm)" package="3 mm [THT]"]
  LED20 = LED - 3mm [color="Red (633nm)" package="3 mm [THT]"]
  LED21 = LED - 3mm [color="Red (633nm)" package="3 mm [THT]"]
  LED22 = LED - 3mm [color="Red (633nm)" package="3 mm [THT]"]
  LED23 = LED - 3mm [color="Red (633nm)" package="3 mm [THT]"]
  LED24 = LED - 3mm [color="Red (633nm)" package="3 mm [THT]"]
  LED25 = LED - 3mm [color="Red (633nm)" package="3 mm [THT]"]
  LED26 = LED - 3mm [color="Red (633nm)" package="3 mm [THT]"]
  LED27 = LED - 3mm [color="Red (633nm)" package="3 mm [THT]"]
  LED28 = LED - 3mm [color="Red (633nm)" package="3 mm [THT]"]
  LED29 = LED - 3mm [color="Red (633nm)" package="3 mm [THT]"]
  LED30 = LED - 3mm [color="Red (633nm)" package="3 mm [THT]"]
  LED31 = LED - 3mm [color="Red (633nm)" package="3 mm [THT]"]
  LED32 = LED - 3mm [color="Red (633nm)" package="3 mm [THT]"]
  IC9 = IC, DIP package, 8 pins [chip_label=IC spacing=300mil]
  J3 = female pin header, 2 pins [form="♀ (female)"]
  J7 = female pin header, 2 pins [form="♀ (female)"]
  J8 = female pin header, 2 pins [form="♀ (female)"]
  J9 = female pin header, 2 pins [form="♀ (female)" part_number=gnd]
  J10 = female pin header, 2 pins [form="♀ (female)"]
  J11 = female pin header, 2 pins [form="♀ (female)"]
  R20 = Resistor [tolerance=±5% resistance=220 package=THT]

nets:
  N1: IC1.pin2, R4.Pin_0
  N2: IC1.pin3, IC2.pin3, IC3.pin3, IC4.pin3, IC5.pin3, IC6.pin3, IC7.pin3, IC8.pin3, IC9.pin2, J11.pin1, J11.pin2
  N3: IC1.pin4, LED1.anode, LED2.anode, LED4.anode, LED3.anode, IC2.pin4, LED5.anode, LED6.anode, LED7.anode, LED8.anode, IC3.pin4, IC4.pin4, LED9.anode, LED10.anode, LED11.anode, LED12.anode, LED13.anode, LED14.anode, LED15.anode, LED16.anode, IC5.pin4, IC6.pin4, IC7.pin4, IC8.pin4, LED17.anode, LED18.anode, LED19.anode, LED20.anode, LED21.anode, LED22.anode, LED23.anode, LED24.anode, LED25.anode, LED26.anode, LED27.anode, LED28.anode, LED29.anode, LED30.anode, LED31.anode, LED32.anode, IC9.pin4, J8.pin2, J9.pin1, J9.pin2
  N4: IC1.pin5, R3.Pin_0
  N5: IC1.pin6, R2.Pin_0
  N6: IC1.pin7, R1.Pin_0
  N7: IC1.pin8, IC2.pin8, IC3.pin8, IC4.pin8, IC5.pin8, IC6.pin8, IC7.pin8, IC8.pin8, IC9.pin8, J3.pin2, J10.pin1, J10.pin2
  N8: R1.Pin_1, LED3.cathode
  N9: R2.Pin_1, LED2.cathode
  N10: R4.Pin_1, LED4.cathode
  N11: LED1.cathode, R3.Pin_1
  N12: IC2.pin2, R8.Pin_0
  N13: IC2.pin5, R5.Pin_0
  N14: IC2.pin6, R7.Pin_0
  N15: IC2.pin7, R6.Pin_0
  N16: R5.Pin_1, LED5.cathode
  N17: R6.Pin_1, LED8.cathode
  N18: R7.Pin_1, LED6.cathode
  N19: R8.Pin_1, LED7.cathode
  N20: IC3.pin2, R15.Pin_0
  N21: IC3.pin5, R9.Pin_0
  N22: IC3.pin6, R13.Pin_0
  N23: IC3.pin7, R11.Pin_0
  N24: IC4.pin2, R16.Pin_0
  N25: IC4.pin5, R10.Pin_0
  N26: IC4.pin6, R14.Pin_0
  N27: IC4.pin7, R12.Pin_0
  N28: R9.Pin_1, LED9.cathode
  N29: R10.Pin_1, LED10.cathode
  N30: R11.Pin_1, LED15.cathode
  N31: R12.Pin_1, LED16.cathode
  N32: R13.Pin_1, LED11.cathode
  N33: R14.Pin_1, LED12.cathode
  N34: R15.Pin_1, LED13.cathode
  N35: R16.Pin_1, LED14.cathode
  N36: IC5.pin2, R29.Pin_0
  N37: IC5.pin5, R17.Pin_0
  N38: IC5.pin6, R25.Pin_0
  N39: IC5.pin7, R21.Pin_0
  N40: IC6.pin2, R30.Pin_0
  N41: IC6.pin5, R18.Pin_0
  N42: IC6.pin6, R26.Pin_0
  N43: IC6.pin7, R22.Pin_0
  N44: IC7.pin2, R31.Pin_0
  N45: IC7.pin5, R19.Pin_0
  N46: IC7.pin6, R27.Pin_0
  N47: IC7.pin7, R23.Pin_0
  N48: IC8.pin2, R32.Pin_0
  N49: IC8.pin5, R20.Pin_0
  N50: IC8.pin6, R28.Pin_0
  N51: IC8.pin7, R24.Pin_0
  N52: R17.Pin_1, LED17.cathode
  N53: R18.Pin_1, LED18.cathode
  N54: R19.Pin_1, LED19.cathode
  N55: R21.Pin_1, LED29.cathode
  N56: R22.Pin_1, LED30.cathode
  N57: R23.Pin_1, LED31.cathode
  N58: R24.Pin_1, LED32.cathode
  N59: R25.Pin_1, LED21.cathode
  N60: R26.Pin_1, LED22.cathode
  N61: R27.Pin_1, LED23.cathode
  N62: R28.Pin_1, LED24.cathode
  N63: R29.Pin_1, LED25.cathode
  N64: R30.Pin_1, LED26.cathode
  N65: R31.Pin_1, LED27.cathode
  N66: R32.Pin_1, LED28.cathode
  N67: LED20.cathode, R20.Pin_1
  N68: IC9.pin1, J8.pin1
  N69: IC9.pin5, J7.pin2
  N70: IC9.pin6, J7.pin1
  N71: IC9.pin7, J3.pin1

notes:
  mi
  rs
  v+
  mo
  gnd
  V+
  ser
  gd
  sc
  Genals
  POV
