# Fritzing sketch id3097_sharePower33_0 (saved by Fritzing 0.3.8b)
breadboards: 1

parts:
  J1 = Screw terminal [package=THT]
  J2 = Screw terminal [package=THT]
  U1 = Voltage Regulator -- 3.3 V -- LM1117
  C2 = Tantalum Capacitor [package=THT]
  C3 = Tantalum Capacitor [package=THT]

nets:
  N1: J1.pin1, J2.pin2, U1.connector0, C2.-, C3.-
  N2: J1.pin2, U1.connector2, C2.+
  N3: J2.pin1, U1.connector1, C3.+

notes:
  +V in -->
  in gnd -->
  <-- +3.3 V out
  <-- out gnd
