# Fritzing sketch id3098_quad_power_dsitrobution_III_0 (saved by Fritzing 0.7.11b)
breadboards: 1

parts:
  data = molex pin header, 4 pins [form=molex]
  esc3 = molex pin header, 3 pins [form=molex]
  esc2 = molex pin header, 3 pins [form=molex]
  esc1 = molex pin header, 3 pins [form=molex]
  esc4 = molex pin header, 3 pins [form=molex]
  +5_v_ADFM_2_5 = Pad [width=6 height=6 connect=center]
  +_battery = Pad [width=6 height=9 connect=center]
  +_motor_4 = Pad [width=6 height=9 connect=center]
  +_motor_3 = Pad [width=6 height=9 connect=center]
  +_motor_2 = Pad [width=6 height=9 connect=center]
  +_motor_1 = Pad [width=6 height=9 connect=center]
  +_-_AFM = double row female pin header, 2 pins [form="♀ (female)"]

nets:
  N1: data.pin1, esc4.pin1
  N2: data.pin2, esc3.pin1
  N3: data.pin3, esc2.pin1
  N4: data.pin4, esc1.pin1
  N5: esc3.pin2, esc2.pin2, esc1.pin2, esc4.pin2, +5_v_ADFM_2_5.pad, +_-_AFM.pin2
  N6: +_battery.pad, +_motor_4.pad, +_motor_3.pad, +_motor_2.pad, +_motor_1.pad

notes:
  Quad Power Distro MKIII
