# Fritzing sketch id3099_Power_interface_0 (saved by Fritzing 0.7.10b)
breadboards: 1

parts:
  J1 = Basic Servo
  J2 = Basic Servo
  J3 = Basic Servo
  J4 = Basic Servo
  C1 = Ceramic Capacitor [capacitance=100nF package="200 mil [THT, multilayer]"]
  C2 = Ceramic Capacitor [capacitance=100nF package="200 mil [THT, multilayer]"]
  C3 = Ceramic Capacitor [capacitance=100nF package="200 mil [THT, multilayer]"]
  C4 = Ceramic Capacitor [capacitance=100nF package="200 mil [THT, multilayer]"]
  U1 = Voltage Regulator - 5V [package="TO220 [THT]"]
  U2 = Voltage Regulator - 5V [package="TO220 [THT]"]
  U3 = Voltage Regulator - 5V [package="TO220 [THT]"]
  U4 = Voltage Regulator - 5V [package="TO220 [THT]"]
  VCC1 = Battery block 9V
  C7 = Ceramic Capacitor [capacitance=330nF package="200 mil [THT, multilayer]"]
  C6 = Ceramic Capacitor [capacitance=330nF package="200 mil [THT, multilayer]"]
  C8 = Ceramic Capacitor [capacitance=330nF package="200 mil [THT, multilayer]"]
  C5 = Ceramic Capacitor [capacitance=330nF package="200 mil [THT, multilayer]"]
  Arduino1 = Arduino  # not connected

nets:
  GND: J1.gnd, J2.gnd, J3.gnd, J4.gnd, C1.0, C2.0, C3.1, C4.0, U1.GND, U2.GND, U3.GND, U4.GND, VCC1.-, C7.1, C6.1, C8.1, C5.1
  N1: J1.vcc, C3.0, U1.output_voltage
  N2: J2.vcc, C4.1, U3.output_voltage
  N3: J3.vcc, C2.1, U4.output_voltage
  N4: J4.vcc, C1.1, U2.output_voltage
  N5: U1.input_voltage, U2.input_voltage, U3.input_voltage, U4.input_voltage, VCC1.+, C7.0, C6.0, C8.0, C5.0
