# Fritzing sketch id30_10_segment_led (saved by Fritzing 0.4.3b)
breadboards: 1

parts:
  Netduino1 = Netduino
  LED1 = yellow LED - 5mm
  R1 = 100 Ω Resistor [package=THT]
  R1_2 = 100 Ω Resistor [package=THT]
  R1_3 = 100 Ω Resistor [package=THT]
  R1_4 = 100 Ω Resistor [package=THT]
  R1_5 = 100 Ω Resistor [package=THT]
  R1_6 = 100 Ω Resistor [package=THT]
  R1_7 = 100 Ω Resistor [package=THT]
  R1_8 = 100 Ω Resistor [package=THT]
  R1_9 = 100 Ω Resistor [package=THT]
  R1_10 = 100 Ω Resistor [package=THT]
  LED1_2 = yellow LED - 5mm
  LED1_3 = yellow LED - 5mm
  LED1_4 = yellow LED - 5mm
  LED1_5 = yellow LED - 5mm
  LED1_6 = yellow LED - 5mm
  LED1_7 = yellow LED - 5mm
  LED1_8 = yellow LED - 5mm
  LED1_9 = yellow LED - 5mm
  LED1_10 = yellow LED - 5mm

nets:
  N1: Netduino1.3V3, R1.Pin_1, R1_2.Pin_1, R1_3.Pin_1, R1_4.Pin_1, R1_5.Pin_1, R1_6.Pin_1, R1_7.Pin_1, R1_8.Pin_1, R1_9.Pin_1, R1_10.Pin_1
  N2: Netduino1.GND, LED1.cathode, LED1_2.cathode, LED1_3.cathode, LED1_4.cathode, LED1_5.cathode, LED1_6.cathode, LED1_7.cathode, LED1_8.cathode, LED1_9.cathode, LED1_10.cathode
  N3: LED1.anode, R1.Pin_0
  N4: R1_2.Pin_0, LED1_2.anode
  N5: R1_3.Pin_0, LED1_3.anode
  N6: R1_4.Pin_0, LED1_4.anode
  N7: R1_5.Pin_0, LED1_5.anode
  N8: R1_6.Pin_0, LED1_6.anode
  N9: R1_7.Pin_0, LED1_7.anode
  N10: R1_8.Pin_0, LED1_8.anode
  N11: R1_9.Pin_0, LED1_9.anode
  N12: R1_10.Pin_0, LED1_10.anode
