# Fritzing sketch id3100_Voltage_Chooser_0 (saved by Fritzing 0.9.3b)
circuit board: 2.80424cm x 2.34225cm
breadboards: 1

parts:
  L7805 = Voltage Regulator - 5V [package="TO220 [THT]"]
  C2 = Ceramic Capacitor [capacitance=1µF package="100 mil [THT, multilayer]"]
  C3 = Ceramic Capacitor [capacitance=1µF package="100 mil [THT, multilayer]"]
  C4 = Ceramic Capacitor [capacitance=1µF package="100 mil [THT, multilayer]"]
  9V = Battery block 9V
  Switch = Toggle Switch [package=THT]
  LM1117 = Voltage Regulator -- 3.3 V -- LM1117
  5V1 = female pin header, 4 pins [form="♀ (female)"]

nets:
  N1: L7805.input_voltage, Switch.L2
  N2: L7805.GND, C2.0, C3.0, C4.0, 9V.-, LM1117.connector0, 5V1.pin4
  N3: L7805.output_voltage, C2.1, 5V1.pin2
  N4: C3.1, 9V.+, Switch.COM, 5V1.pin1
  N5: C4.1, LM1117.connector1, 5V1.pin3
  N6: Switch.L1, LM1117.connector2

notes:
  9V
  5V
  3.3V
  GND
  W.A. ten Brink
