# Fritzing sketch id3101_WemosTelegram_0 (saved by Fritzing 0.9.3b)
breadboards: 1

parts:
  WeMos_D1_Mini1 = WeMos D1 Mini
  U1 = RELAY-SOLIDSTATE [package=relay-s108t02]
  RGB_LED = RGB LED (com. cathode, rgb) [package="5 mm [THT]"]
  R1 = Resistor [tolerance=±5% resistance=220 package="0402 [SMD]"]
  R2 = Resistor [tolerance=±5% resistance=220 package="0402 [SMD]"]  # not connected
  230V~ = AC Power [frequency=60]

nets:
  N1: WeMos_D1_Mini1.D0, U1.+
  N2: WeMos_D1_Mini1.D5, RGB_LED.blue_anode
  N3: WeMos_D1_Mini1.D6, RGB_LED.green_anode
  N4: WeMos_D1_Mini1.D7, RGB_LED.red_anode
  N5: WeMos_D1_Mini1.G, R1.Pin_1
  N6: U1.T1, 230V~.V+
  N7: U1.-, R1.Pin_0

notes:
  Solid state relay g3mb-202p has R1 build in.
