# Fritzing sketch id3102_4N35_0 (saved by Fritzing 0.8.7b)
breadboards: 1

parts:
  Parte1 = Arduino Uno (Rev3)
  U1 = Optocoupler [package=THT]
  R1 = Resistor [tolerance=±5% resistance=220 package=THT]
  J1 = screw terminal, 3 pins

nets:
  N1: Parte1.D5_PWM, R1.Pin_0
  N2: Parte1.5V, J1.pin1
  N3: Parte1.GND, U1.Pin_2, U1.Pin_4, J1.pin3
  N4: U1.Pin_1, R1.Pin_1
  N5: U1.Pin_5, J1.pin2
