# Fritzing sketch id3103_HelloWorld_0 (saved by Fritzing 0.9.3b)
circuit board: 5cm x 3cm
breadboards: 1

parts:
  VCC1 = Battery block 9V [part_number=Pwr]
  R1 = Resistor [tolerance=±5% resistance=470 part_number="R 1" package=THT]
  LED1 = LED - 5mm [color="Red (633nm)" part_number="LED 1" package="5 mm [THT]"]
  Arduino_Nano = Arduino Nano (Rev3.0) [part_number="Arduino Nano 1"]

nets:
  N1: VCC1.-, LED1.cathode, Arduino_Nano.GND
  N2: VCC1.+, Arduino_Nano.VIN
  N3: R1.Pin_0, LED1.anode
  N4: R1.Pin_1, Arduino_Nano.D10
