# Fritzing sketch id3106_pr4403v2_0 (saved by Fritzing 0.9.2b)
circuit board: 2.45605cm x 1.11709cm
breadboards: 1

parts:
  IC1 = SO08 [chip_label=IC package=SO]
  L1 = Inductor [package="1206 [SMD]"]
  J1 = female pin header, 2 pins [form="♀ (female)"]
  J2 = female pin header, 2 pins [form="♀ (female)"]
  D1 = Rectifier Diode [part_number=1N4001 package="300 mil [THT]"]
  J3 = female pin header, 1 pin [form="♀ (female)"]
  J4 = female pin header, 1 pin [form="♀ (female)"]
  R1 = Resistor [tolerance=±5% resistance=330 package="1206 [SMD]"]

nets:
  N1: IC1.2, R1.Pin_1
  N2: IC1.3, IC1.6, L1.pin_1, J2.pin1
  N3: IC1.5, J1.pin2, J2.pin2, J4.pin1
  N4: IC1.8, L1.pin_0, D1.cathode, J3.pin1
  N5: J1.pin1, D1.anode, R1.Pin_0

notes:
  D.Ernst
  PR4403
  Solar
