# Fritzing sketch id3107_practica2_0 (saved by Fritzing 0.9.3b)
breadboards: 1

parts:
  Raspberry_Pi1 = Raspberry Pi 2
  LED1 = smd LED [color="Red (633nm)" package="0603 [SMD]"]
  R1 = Resistor [tolerance=±5% resistance=330 package="1206 [SMD]"]
  S1 = Round Pushbutton

nets:
  N1: Raspberry_Pi1.GND, LED1.cathode, S1.leg1
  N2: Raspberry_Pi1.GPIO24, S1.leg0
  N3: Raspberry_Pi1.GPIO23, R1.Pin_1
  N4: LED1.anode, R1.Pin_0
