# Fritzing sketch id3108_Practica1_Secuencia_Monasterio_0 (saved by Fritzing 0.9.3b)
breadboards: 1

parts:
  Componente1 = Arduino Uno (Rev3)
  R1 = Resistor [tolerance=±5% resistance=220 package=THT]
  R2 = Resistor [tolerance=±5% resistance=220 package=THT]
  R3 = Resistor [tolerance=±5% resistance=220 package=THT]
  R4 = Resistor [tolerance=±5% resistance=220 package=THT]
  R5 = Resistor [tolerance=±5% resistance=220 package=THT]  # not connected
  R6 = Resistor [tolerance=±5% resistance=220 package=THT]
  LED1 = LED - 5mm [color="Red (633nm)" package="5 mm [THT]"]
  LED2 = LED - 5mm [color="Red (633nm)" package="5 mm [THT]"]
  LED6 = smd LED [color="Yellow (585nm)" package="1206 [SMD]"]
  LED7 = smd LED [color="Yellow (585nm)" package="1206 [SMD]"]
  LED12 = smd LED [color="Green (555nm)" package="1206 [SMD]"]
  LED13 = smd LED [color="Green (555nm)" package="1206 [SMD]"]

nets:
  N1: Componente1.D8, LED12.anode
  N2: Componente1.D9_PWM, LED13.anode
  N3: Componente1.D4, LED1.anode
  N4: Componente1.D5_PWM, LED2.anode
  N5: Componente1.D6_PWM, LED6.anode
  N6: Componente1.D7, LED7.anode
  N7: Componente1.GND, R1.Pin_0, R2.Pin_0, R3.Pin_0, R4.Pin_0, R6.Pin_0
  N8: R1.Pin_1, LED1.cathode
  N9: R2.Pin_1, LED2.cathode
  N10: R3.Pin_1, LED6.cathode
  N11: R4.Pin_1, LED7.cathode
  N12: R6.Pin_1, LED13.cathode
