# Fritzing sketch id3109_preamp_electret_opamp_0 (saved by Fritzing 0.8.3b)
circuit board: 4.16744cm x 2.82927cm
breadboards: 1

parts:
  MIC1 = Microphone
  R1 = Resistor [tolerance=±5% resistance=10k package=THT]
  C1 = Electrolytic Capacitor [capacitance=10µF package="100 mil [THT, electrolytic]"]
  U1 = LM 358 Dual Op-Amp [package="DIP8 [THT]"]
  R3 = Resistor [tolerance=±5% resistance=47k package=THT]
  R4 = Resistor [tolerance=±5% resistance=10k package=THT]
  C2 = Electrolytic Capacitor [capacitance=10µF package="100 mil [THT, electrolytic]"]
  R2 = Resistor [tolerance=±5% resistance=10k package=THT]
  R7 = Resistor [tolerance=±5% resistance=47k package=THT]
  C3 = Electrolytic Capacitor [capacitance=10µF package="100 mil [THT, electrolytic]"]
  R8 = Resistor [tolerance=±5% resistance=10k package=THT]
  C4 = Electrolytic Capacitor [capacitance=10µF package="100 mil [THT, electrolytic]"]
  MIC2 = Microphone
  BAT1 = Battery Holders [package=battcom_20mm_pth]
  R9 = Resistor [tolerance=±5% resistance=10k package=THT]
  R10 = Resistor [tolerance=±5% resistance=10k package=THT]
  TRS1 = Audio Jack (TRS) 3.5mm [package="4Ucon 08780 [THT]"]

nets:
  GND: MIC1.pin1, U1.connector3, R2.Pin_0, MIC2.pin1, BAT1.-, TRS1.Sleeve
  N1: MIC1.pin2, C1.+, R9.Pin_1
  5V: R1.Pin_0, U1.connector7, BAT1.+, R9.Pin_0, R10.Pin_1
  N2: R1.Pin_1, U1.connector2, U1.connector4, R2.Pin_1
  N3: C1.-, R4.Pin_1
  N4: U1.connector0, R3.Pin_0, C2.+
  N5: U1.connector1, R3.Pin_1, R4.Pin_0
  N6: U1.connector5, R7.Pin_1, R8.Pin_0
  N7: U1.connector6, R7.Pin_0, C3.+
  N8: C2.-, TRS1.Tip
  N9: C3.-, TRS1.Ring
  N10: R8.Pin_1, C4.-
  N11: C4.+, MIC2.pin2, R10.Pin_0
