# Fritzing sketch id310_projeto_teste_0 (saved by Fritzing 0.9.2b)
breadboards: 1

parts:
  Componente1 = Arduino Uno (Rev3)
  BMP1 = BMP085_Breakout
  DHT1 = DHT22_Humidity_and_Temperature_Sensor
  R1 = Resistor [tolerance=±5% resistance=10k package=THT]
  GPS1 = Adafruit_Ultimate_GPS_Breakout
  U1 = XBEE-1 [package=xbee-1]

nets:
  N1: Componente1.A4/SDA, BMP1.connector4
  N2: Componente1.A5/SCL, BMP1.connector3
  N3: Componente1.D0/RX, U1.DOUT
  N4: Componente1.D1/TX, U1.DIN
  N5: Componente1.D2, DHT1.connector2, R1.Pin_0
  N6: Componente1.D5_PWM, GPS1.connector5
  N7: Componente1.D6_PWM, GPS1.connector6
  5V: Componente1.5V, BMP1.connector1, DHT1.connector1, R1.Pin_1, GPS1.connector8, U1.VDD
  GND: Componente1.GND, BMP1.connector7, DHT1.connector4, GPS1.connector7, U1.GND
