# Fritzing sketch id3110_preamp_electret_0 (saved by Fritzing 0.8.3b)
circuit board: 4.12041cm x 3.73944cm
breadboards: 1

parts:
  MIC1 = Microphone
  R1 = Resistor [tolerance=±5% resistance=10k package=THT]
  C1 = Electrolytic Capacitor [capacitance=10µF package="100 mil [THT, electrolytic]"]
  U1 = LM 358 Dual Op-Amp [package="DIP8 [THT]"]
  R3 = Resistor [tolerance=±5% resistance=47k package=THT]
  R4 = Resistor [tolerance=±5% resistance=10k package=THT]
  C2 = Electrolytic Capacitor [capacitance=10µF package="100 mil [THT, electrolytic]"]
  JP1 = Header 2 [package=screwterminal-3.5mm-2_lock]
  R2 = Resistor [tolerance=±5% resistance=10k package=THT]
  R5 = Resistor [tolerance=±5% resistance=10k package=THT]
  R6 = Resistor [tolerance=±5% resistance=10k package=THT]
  R7 = Resistor [tolerance=±5% resistance=47k package=THT]
  C3 = Electrolytic Capacitor [capacitance=10µF package="100 mil [THT, electrolytic]"]
  JP2 = Header 2 [package=screwterminal-3.5mm-2_lock]
  R8 = Resistor [tolerance=±5% resistance=10k package=THT]
  C4 = Electrolytic Capacitor [capacitance=10µF package="100 mil [THT, electrolytic]"]
  MIC2 = Microphone
  BAT1 = Battery Holders [package=battcom_20mm_pth]

nets:
  GND: MIC1.pin1, U1.connector3, JP1.1, R2.Pin_0, R6.Pin_0, JP2.1, MIC2.pin1, BAT1.-
  N1: MIC1.pin2, C1.+
  3.3V: R1.Pin_0, U1.connector7, R5.Pin_0, BAT1.+
  N2: R1.Pin_1, U1.connector2, R2.Pin_1
  N3: C1.-, R4.Pin_1
  N4: U1.connector0, R3.Pin_0, C2.+
  N5: U1.connector1, R3.Pin_1, R4.Pin_0
  N6: U1.connector4, R5.Pin_1, R6.Pin_1
  N7: U1.connector5, R7.Pin_1, R8.Pin_0
  N8: U1.connector6, R7.Pin_0, C3.+
  N9: C2.-, JP1.2
  N10: C3.-, JP2.2
  N11: R8.Pin_1, C4.-
  N12: C4.+, MIC2.pin2
