# Fritzing sketch id3113_Untitled_Sketch_2_0 (saved by Fritzing 0.9.2b)
breadboards: 1

parts:
  Part1 = Arduino Uno (Rev3)
  S1 = Pushbutton [package="[THT]"]
  R1 = Resistor [tolerance=±5% resistance=220 package=THT]
  R2 = Resistor [tolerance=±5% resistance=220 package=THT]
  S2 = Pushbutton [package="[THT]"]
  R3 = Resistor [tolerance=±5% resistance=220 package=THT]
  S3 = Pushbutton [package="[THT]"]
  LED1 = RGB LED (com. cathode, rgb) [package="5 mm [THT]"]
  R4 = Resistor [tolerance=±5% resistance=220 package=THT]
  R5 = Resistor [tolerance=±5% resistance=220 package=THT]
  R6 = Resistor [tolerance=±5% resistance=220 package=THT]
  LED2 = RGB LED (com. cathode, rgb) [package="5 mm [THT]"]
  R7 = Resistor [tolerance=±5% resistance=220 package=THT]
  R8 = Resistor [tolerance=±5% resistance=220 package=THT]
  R9 = Resistor [tolerance=±5% resistance=220 package=THT]

nets:
  N1: Part1.D8, R7.Pin_1
  N2: Part1.D9_PWM, R8.Pin_1
  N3: Part1.D10_PWM/SS, R9.Pin_1
  N4: Part1.D11_PWM/MOSI, R5.Pin_1
  N5: Part1.D12/MISO, R6.Pin_1
  N6: Part1.D13/SCK, R4.Pin_1
  N7: Part1.GND, R1.Pin_1, R2.Pin_0, R3.Pin_0
  N8: Part1.D2, S1.Pin_3, S1.Pin_4, R1.Pin_0
  N9: Part1.D3_PWM, R2.Pin_1, S2.Pin_3, S2.Pin_4
  N10: Part1.D4, R3.Pin_1, S3.Pin_3, S3.Pin_4
  N11: Part1.5V, S1.Pin_1, S1.Pin_2, S2.Pin_1, S2.Pin_2, S3.Pin_1, S3.Pin_2
  N12: LED1.red_anode, R4.Pin_0
  N13: LED1.green_anode, R6.Pin_0
  N14: LED1.blue_anode, R5.Pin_0
  N15: LED2.red_anode, R9.Pin_0
  N16: LED2.green_anode, R8.Pin_0
  N17: LED2.blue_anode, R7.Pin_0
