# Fritzing sketch id3114_Led_con_boton2_0 (saved by Fritzing 0.9.2b)
breadboards: 1

parts:
  R1 = Resistor [tolerance=±5% resistance=220 package=THT]
  LED1 = LED - 5mm [color="Red (633nm)" package="5 mm [THT]"]
  Parte1 = Arduino Mega 2560 (Rev3)
  S1 = Pushbutton [package="[THT]"]
  R2 = Resistor [tolerance=±5% resistance=10 package=THT]

nets:
  N1: R1.Pin_0, LED1.anode
  N2: R1.Pin_1, Parte1.D11_PWM
  N3: LED1.cathode, Parte1.GND, R2.Pin_0
  N4: Parte1.D8_PWM, S1.Pin_3, S1.Pin_4, R2.Pin_1
  N5: Parte1.5V, S1.Pin_1, S1.Pin_2

notes:
  Prender un Led con boton
