# Fritzing sketch id3115_BlinkNPress_0 (saved by Fritzing 0.9.0b)
breadboards: 1

parts:
  Part1 = Arduino Uno (Rev3)
  LED1 = LED - 5mm [color="Red (633nm)" package="5 mm [THT]"]
  S1 = Pushbutton [package="[THT]"]
  R1 = Resistor [tolerance=±5% resistance=10k package=THT]
  R2 = Resistor [tolerance=±5% resistance=10k package=THT]
  R3 = Resistor [tolerance=±5% resistance=100 package=THT]

nets:
  N1: Part1.GND, LED1.cathode
  N2: Part1.D2, R3.Pin_1
  N3: Part1.D7, R1.Pin_0
  N4: Part1.5V, R2.Pin_1
  N5: LED1.anode, S1.Pin_3, S1.Pin_4, R1.Pin_1
  N6: S1.Pin_1, S1.Pin_2, R2.Pin_0
