# Fritzing sketch id3116_RPiTemperatureHumidityPressure2_0 (saved by Fritzing 0.9.2b)
breadboards: 1

parts:
  Raspberry_Pi1 = Raspberry Pi B+
  Sensor2 = DHT22_Humidity_and_Temperature_Sensor
  Sensor1 = Barometric Pressure Sensor - BMP085 Breakout
  Part3 = Breadboard Power Supply Board SMD [part_number="5V out"]
  Part4 = Breadboard Power Supply Board SMD [part_number="3.3V out"]
  J1 = Power Jack [package=power_jack_combo]
  R1 = Resistor [tolerance=±5% resistance=4.7k package=THT]
  lvlshift1 = bidilevelconverter [part_number="5V-3.3V bidi"]

nets:
  N1: Raspberry_Pi1.GPIO2, Sensor1.SDA, lvlshift1.connector11
  N2: Raspberry_Pi1.GPIO3, Sensor1.SCL, lvlshift1.connector10
  N3: Raspberry_Pi1.GPIO4, lvlshift1.connector7
  GND: Raspberry_Pi1.GND, Sensor2.connector4, Sensor1.GND, Part3.GND, Part4.GND, J1.GND, lvlshift1.connector2, lvlshift1.connector9
  N4: Sensor2.connector1, Part3.VCC, R1.Pin_0, lvlshift1.connector3
  N5: Sensor2.connector2, R1.Pin_1, lvlshift1.connector4
  VCC: Sensor1.VCC, Part4.VCC, lvlshift1.connector8
  VIN: Part3.VIN, Part4.VIN, J1.PWR

notes:
  9V input from ac-dc converter
  Bi-Directional Level Shifter converts from 3.3V to 5V and back again on the same lines allowing it to be used for a bus
  Note that these sensors do not take much power so they could be powered from the RPi, but I have used external power for cases when I use displays etc.
  This work by hobbyistdave is licensed under a Creative Commons Attribution-ShareAlike 4.0 International License
  No warranty either express or implied is given.
  This schematic was created with Fritzing.
  BMP & DHT Libraries from Adafruit
  www.adafruit.com
  v1, Oct 2015
  4.7kohm pull-up on 1-wire bus
  Barometric Pressure, Temperature and Humidity Monitor
  www.hobbyspot.org
  BMP180 is a 3.3V device
  DHT22 can be 5V or 3.3V
