# Fritzing sketch id3117_Untitled_Sketch_0 (saved by Fritzing 0.9.2b)
breadboards: 1

parts:
  Part1 = Arduino Uno (Rev3)
  J1 = Basic Force Sensing Resistor (FSR) [package=THT]
  R1 = Resistor [tolerance=±5% resistance=220 package=THT]
  R2 = Resistor [tolerance=±5% resistance=220 package=THT]

nets:
  N1: Part1.A0, R2.Pin_0
  N2: Part1.GND, R2.Pin_1
  N3: J1.pin_0, R1.Pin_1

notes:
  pressure transuder
  (circuit connection)
  pressure transuder connection to aurdino uno
  which is used to take readings of pressure output in the hybrid rocket testing that we are going to do.
