# Fritzing sketch id3118_PressureSensor_0 (saved by Fritzing 0.8.7b)
breadboards: 1

parts:
  パーツ1 = Arduino Uno (Rev3)
  R2 = Resistor [package="2512 [SMD]"]
  J1 = Basic Force Sensing Resistor (FSR) [package=THT]
  J2 = Basic Force Sensing Resistor (FSR) [package=THT]
  R3 = Resistor [package="2512 [SMD]"]

nets:
  N1: パーツ1.A1, J1.pin_0, R3.Pin_0
  N2: パーツ1.A2, R2.Pin_0, J2.pin_1
  N3: パーツ1.5V, R2.Pin_1, R3.Pin_1
  N4: パーツ1.GND, J1.pin_1, J2.pin_0
