# Fritzing sketch id3119_Primer_Ejercicio_CNA_0 (saved by Fritzing 0.9.2b)
breadboards: 1

parts:
  LED1 = LED - 5mm [color="Red (633nm)" package="5 mm [THT]"]
  S1 = Pushbutton [package="[THT]"]
  T1 = LM35 Temperature Sensor [package="TO92 [THT]"]
  R1 = Rotary Potentiometer (Small) [maximum_resistance=100kΩ package=THT]
  LED2 = LED - 5mm [color="Red (633nm)" package="5 mm [THT]"]

nets:
  N1: LED1.cathode, R1.leg2
  N2: LED1.anode, T1.GND
  N3: S1.Pin_1, S1.Pin_2, T1.Vout
  N4: S1.Pin_3, S1.Pin_4, T1.+Vs, R1.leg1, LED2.cathode
  N5: R1.wiper, LED2.anode
