# Fritzing sketch id3120_df_player_mini_sensor_0 (saved by Fritzing 0.9.2b)
breadboards: 1

parts:
  DFPlayer_Mini1 = DFPlayer Mini
  SP1 = SPEAKER [package=pcb_mount_speaker]
  R1 = Resistor [tolerance=±5% resistance=1k package=THT]
  부품1 = Arduino Uno (Rev3)
  R2 = Resistor [tolerance=±5% resistance=1k package=THT]
  부품2 = SRF05 Ultrasonic Rangefinder

nets:
  N1: DFPlayer_Mini1.connector0, 부품1.5V, 부품2.connector8
  N2: DFPlayer_Mini1.connector1, R1.Pin_1
  N3: DFPlayer_Mini1.connector2, R2.Pin_1
  N4: DFPlayer_Mini1.connector5, SP1.-
  N5: DFPlayer_Mini1.connector6, 부품1.GND, 부품2.connector11
  N6: DFPlayer_Mini1.connector7, SP1.+
  N7: R1.Pin_0, 부품1.D1/TX
  N8: 부품1.D8, 부품2.connector10
  N9: 부품1.D9_PWM, 부품2.connector9
  N10: 부품1.D0/RX, R2.Pin_0
