# Fritzing sketch id3121_Ejercicio2_0 (saved by Fritzing 0.9.2b)
breadboards: 1

parts:
  Parte1 = Arduino Uno (Rev3)
  LED1 = smd LED [color="Red (633nm)" package="1206 [SMD]"]
  LED2 = smd LED [color="Yellow (585nm)" package="1206 [SMD]"]
  LED3 = smd LED [color="Green (565nm)" package="1206 [SMD]"]
  R1 = Resistor [tolerance=±5% resistance=220 package=THT]
  R2 = Resistor [tolerance=±5% resistance=220 package=THT]
  R3 = Resistor [tolerance=±5% resistance=220 package=THT]
  R4 = Resistor [tolerance=±5% resistance=220 package=THT]
  J1 = Piezo Speaker
  Q1 = NPN-Transistor [package="TO92 [THT]"]

nets:
  N1: Parte1.D9_PWM, LED2.anode
  N2: Parte1.D12/MISO, LED1.anode
  N3: Parte1.D3_PWM, R4.Pin_1
  N4: Parte1.D6_PWM, LED3.anode
  N5: LED1.cathode, R1.Pin_0
  N6: LED2.cathode, R2.Pin_0
  N7: LED3.cathode, R3.Pin_0
  N8: R1.Pin_1, R2.Pin_1, R3.Pin_1, J1.pin2, Q1.C
  N9: J1.pin1, Q1.E
