# Fritzing sketch id3122_problematic_sketch_0 (saved by Fritzing 0.9.2b)

parts:
  Part1 = Arduino Uno (Rev3)
  J1 = Basic Servo
  J2 = Basic Servo
  J3 = Basic Servo
  J4 = Basic Servo
  VCC1 = 4 x AAA Battery Mount  # not connected

nets:
  N1: Part1.D9_PWM, J2.pulse
  N2: Part1.D10_PWM/SS, J3.pulse
  N3: Part1.D11_PWM/MOSI, J4.pulse
  GND: Part1.GND, J1.gnd
  N4: Part1.D3_PWM, J1.pulse
