# Fritzing sketch id3123_Progetto_PIR_con_accensione_LED_0 (saved by Fritzing 0.9.1b)
breadboards: 1

parts:
  Raspberry_Pi1 = Raspberry Pi B+
  PIR1 = PIR_sensor
  LED2 = smd LED [color="Red (633nm)" package="1206 [SMD]"]

nets:
  N1: Raspberry_Pi1.GPIO17, PIR1.connector2
  N2: Raspberry_Pi1.GND, PIR1.connector3, LED2.anode
  N3: Raspberry_Pi1.GPIO18, LED2.cathode
  N4: Raspberry_Pi1.5V, PIR1.connector1
