# Fritzing sketch id3124_progetto_tesatacalda_0 (saved by Fritzing 0.9.3b)
circuit board: 11.263cm x 8.14443cm

parts:
  Processore_capo = Arduino Uno (Rev3)
  LED_GRR = DUO LED RG [package="5 mm [THT]"]
  GRR = RELAY [package=relay-jzc]
  R1 = Resistor [tolerance=±5% resistance=220 package=THT]
  R2 = Resistor [tolerance=±5% resistance=220 package=THT]
  S1 = Header 1 [package=1x01_offset]
  S1- = Header 1 [package=1x01_offset]
  S1+ = Header 1 [package=1x01_offset]
  MODE = Momentary Switch [package=ksa_sealed_tac_switch]
  R3 = Resistor [tolerance=±5% resistance=220 package=THT]
  P- = Momentary Switch [package=ksa_sealed_tac_switch]
  P+ = Momentary Switch [package=ksa_sealed_tac_switch]
  R4 = Resistor [tolerance=±5% resistance=220 package=THT]
  R5 = Resistor [tolerance=±5% resistance=220 package=THT]
  GRR-PWR = Header 1 [package=1x01_offset]
  LCD = Header 6 [package=1x06-smd]
  LED_emergency = LED - 5mm [color="Red (633nm)" package="5 mm [THT]"]
  JP1 = Header 3 [package=molex-1x3_lock]
  EMERGENCY = Header 2 [package=jst-2-pth-kit]
  GRR-GND = Header 1 [package=1x01_offset]
  Alimentazione_resistenze = Power Jack [package=power_jack_pth]

nets:
  N1: Processore_capo.D8, R4.Pin_1
  N2: Processore_capo.D9_PWM, R5.Pin_1
  N3: Processore_capo.D10_PWM/SS, R3.Pin_1
  N4: Processore_capo.D11_PWM/MOSI, LCD.5
  N5: Processore_capo.D12/MISO, LCD.6
  N6: Processore_capo.D13/SCK, LED_emergency.anode
  N7: Processore_capo.GND, R1.Pin_1, R2.Pin_1
  N8: Processore_capo.D2, LCD.1
  N9: Processore_capo.D3_PWM, LCD.2
  N10: Processore_capo.D4, LCD.3
  N11: Processore_capo.D5_PWM, LCD.4
  N12: Processore_capo.D6_PWM, GRR.COIL1, JP1.1
  N13: Processore_capo.D7, S1.1
  N14: LED_GRR.red_anode, GRR.NO
  N15: LED_GRR.common_cathode, Alimentazione_resistenze.PWR
  N16: LED_GRR.green_anode, GRR.NC
  N17: GRR.COIL2, R1.Pin_0, JP1.3
  N18: GRR.MAIN, GRR-PWR.1, JP1.2
  N19: R2.Pin_0, S1-.1
  5V: S1+.1, MODE.1, P-.1, P+.1
  N20: MODE.3, R3.Pin_0
  N21: P-.3, R4.Pin_0
  N22: P+.3, R5.Pin_0
  N23: LED_emergency.cathode, EMERGENCY.2
  GND: EMERGENCY.1
  N24: GRR-GND.1, Alimentazione_resistenze.GNDBREAK
