# Fritzing sketch id3125_20161026_2 (saved by Fritzing 0.9.3b)
breadboards: 1

parts:
  U1 = TA7291P
  U2 = TA7291P
  부품1 = Arduino Board Ethernet
  VCC1 = Battery block 9V
  M1 = DC Motor
  M2 = DC Motor
  J1 = Infrared Proximity Sensor
  Pressure_sensor = Textile Analog Pressure Sensor [part_number=PW073]
  J2 = Infrared Proximity Sensor

nets:
  GND: U1.connector1, U2.connector1, 부품1.GND, VCC1.-, J1.GND, Pressure_sensor.pin_1, J2.GND
  N1: U1.connector2, M1.pin_2
  N2: U1.connector4, 부품1.D12/MISO
  N3: U1.connector5, 부품1.D2_PWM
  N4: U1.connector6, 부품1.D3_PWM
  N5: U1.connector7, U2.connector7, 부품1.VIN
  N6: U1.connector8, U2.connector8, VCC1.+
  N7: U1.connector10, M1.pin_1
  N8: U2.connector2, M2.pin_2
  N9: U2.connector4, 부품1.D13/SCK
  N10: U2.connector5, 부품1.D4
  N11: U2.connector6, 부품1.D5_PWM
  N12: U2.connector10, M2.pin_1
  N13: 부품1.A0, J1.Vout
  N14: 부품1.A1, Pressure_sensor.pin_0
  N15: 부품1.A2, J2.Vout
  VCC: 부품1.5V, J1.Vcc, J2.Vcc
