# Fritzing sketch id3125_Key_Optocoupler_0 (saved by Fritzing 0.8.5b)
breadboards: 1

parts:
  BeagleBone1 = BeagleBone_Black
  R2 = Resistor [tolerance=±5% resistance=1k package=THT]
  Optokuppler1 = TLP621 [package=THT]

nets:
  N1: BeagleBone1.connector102, R2.Pin_1, Optokuppler1.Pin_4
  N2: BeagleBone1.connector112, Optokuppler1.Pin_1
  N3: R2.Pin_0, Optokuppler1.Pin_2
