# Fritzing sketch id3126_Key_Transistor_0 (saved by Fritzing 0.8.5b)
breadboards: 1

parts:
  BeagleBone1 = BeagleBone_Black
  R2 = Resistor [tolerance=±5% resistance=1k package=THT]
  Q1 = NPN-Transistor [package="TO92 [THT]"]

nets:
  N1: BeagleBone1.connector102, R2.Pin_1
  N2: BeagleBone1.connector112, Q1.B
  N3: R2.Pin_0, Q1.E
