# Fritzing sketch id3127_Programmer_for_ATtiny85_with_arduino_0 (saved by Fritzing 0.9.0b)
breadboards: 1

parts:
  Componente1 = Arduino Uno (Rev3)
  U1 = attiny85 [package=dip]  # not connected
  R1 = Resistor [tolerance=±5% resistance=220 package="0805 [SMD]"]
  C1 = Electrolytic Capacitor [capacitance=10µF package="1010 [SMD, electrolytic]"]
  LED1 = smd LED [color="Red (633nm)" package="0805 [SMD]"]

nets:
  N1: Componente1.D11_PWM/MOSI, R1.Pin_1
  N2: Componente1.RESET, C1.+
  N3: Componente1.5V, LED1.anode
  N4: Componente1.GND, C1.-
  N5: R1.Pin_0, LED1.cathode

notes:
  ATtiny85
  10 micro
  tested with Arduino IDE 1.5.6-r2
