# Fritzing sketch id3128_rpi_arduino_LLC_bb_0 (saved by Fritzing 0.8.7b)
breadboards: 1

parts:
  Componente1 = Logic Level Converter  # not connected
  RaspberryPi1 = Raspberry_Pi_Model_B  # not connected
  U1 = atmega328 [package=dip]
  S1 = Momentary Switch [package=ksa_sealed_tac_switch]
  XTAL1 = Crystal [frequency="16 Mhz" package=THT]
  C1 = Capacitor [package=cap-pth-small2]
  C2 = Capacitor [package=cap-pth-small2]
  R1 = Resistor [tolerance=±5% resistance=1k package=THT]

nets:
  N1: U1.RESET, S1.2, R1.Pin_1
  N2: U1.VCC, U1.AVCC, U1.AREF, R1.Pin_0
  N3: U1.GND, S1.4, C1.2, C2.2
  N4: U1.XLAT1, XTAL1.pin_0, C2.1
  N5: U1.XLAT2, XTAL1.pin_1, C1.1

notes:
  External 5v power
  Level converter is:
  https://www.sparkfun.com/products/11978
