# Fritzing sketch id312_meb_ampel_0 (saved by Fritzing 0.9.2b)
circuit board: 8.46667cm x 5.64444cm
breadboards: 1

parts:
  Widerstand = Resistor [tolerance=±5% resistance=220 package=THT]
  LED_Rot = LED - 5mm [color="Red (633nm)" package="5 mm [THT]"]
  Schiebeschalter = Toggle Switch [package=THT]
  LED_Grün = LED - 5mm [color="Green (555nm)" package="5 mm [THT]"]

nets:
  4.5V: Widerstand.Pin_0
  N1: Widerstand.Pin_1, Schiebeschalter.COM
  GND: LED_Rot.cathode, LED_Grün.cathode
  N2: LED_Rot.anode, Schiebeschalter.L2
  N3: Schiebeschalter.L1, LED_Grün.anode
