# Fritzing sketch id3130_ATTiny_programming_with_Arduino_Micro_1_0 (saved by Fritzing 0.8.7b)
breadboards: 1

parts:
  Bauteil1 = Arduino Micro (Rev3)  # not connected
  U1 = attiny85 [package=dip]
  U3 = atmel

nets:
  N1: U1.Pin_1, U3.connector0
  N2: U1.Pin_4, U3.connector9
  N3: U1.Pin_5, U3.connector16
  N4: U1.Pin_6, U3.connector17
  N5: U1.Pin_7, U3.connector18
  N6: U1.Pin_8, U3.connector19

notes:
  ATTiny programming with Arduino Micro
  To program an ATTiny, you can use the Arduino ISP sketch, but replace "#define RESET SS" by "#define RESET 10".
