# Fritzing sketch id3133_USA_0 (saved by Fritzing 0.9.2b)
circuit board: 5.31248cm x 6.41269cm

parts:
  LM35 = LM35 Temperature Sensor [package="TO92 [THT]"]
  WS2812 = RGB LED (com. cathode, rbg) [package="5 mm [THT]"]
  30 = LED - 5mm [color="Red (633nm)" package="5 mm [THT]"]
  26 = LED - 5mm [color="Red (633nm)" package="5 mm [THT]"]
  22 = LED - 5mm [color="Green (555nm)" package="5 mm [THT]"]
  28 = LED - 5mm [color="Green (555nm)" package="5 mm [THT]"]
  24 = LED - 5mm [color="Yellow (585nm)" package="5 mm [THT]"]
  Bauteil1 = Arduino Mega 2560 (Rev3)
  DI1 = 7 Segment Display [part_number="SC 39-11 RT"]
  21 = Momentary Switch [package=ksa_sealed_tac_switch]
  J1 = female pin header, 3 pins [form="♀ (female)"]
  Switch = DIP SWITCH [package=dipswitch-02]
  R4 = Resistor [tolerance=±5% resistance=330 package=THT]
  5 = LED - 5mm [color="Red (633nm)" package="5 mm [THT]"]
  330-R7 = Resistor [tolerance=±5% resistance=330 package=THT]
  330-R6 = Resistor [tolerance=±5% resistance=330 package=THT]
  330-R8 = Resistor [tolerance=±5% resistance=330 package=THT]
  330-R5 = Resistor [tolerance=±5% resistance=330 package=THT]
  330-R4 = Resistor [tolerance=±5% resistance=330 package=THT]
  330-R3 = Resistor [tolerance=±5% resistance=330 package=THT]
  330-R2 = Resistor [tolerance=±5% resistance=330 package=THT]
  330-R1 = Resistor [tolerance=±5% resistance=330 package=THT]
  R1 = Resistor [tolerance=±5% resistance=330 package=THT]
  R2 = Resistor [tolerance=±5% resistance=10k package=THT]
  R3 = Resistor [tolerance=±5% resistance=10k package=THT]

nets:
  N1: LM35.+Vs, WS2812.blue_anode, Bauteil1.5V, 21.1, 21.2, J1.pin1, Switch.3, Switch.4
  N2: LM35.Vout, Bauteil1.A9
  GND: LM35.GND, WS2812.common_cathode, 30.cathode, 26.cathode, 22.cathode, 28.cathode, 24.cathode, Bauteil1.GND, DI1.common_cathode, J1.pin2, 5.cathode, R1.Pin_1, R2.Pin_1, R3.Pin_1
  N3: WS2812.red_anode, J1.pin3
  N4: WS2812.green_anode, R4.Pin_0
  N5: 30.anode, Bauteil1.D30
  N6: 26.anode, Bauteil1.D26
  N7: 22.anode, Bauteil1.D22
  N8: 28.anode, Bauteil1.D28
  N9: 24.anode, Bauteil1.D24
  N10: Bauteil1.A8, R4.Pin_1
  N11: Bauteil1.D21/SCL, 21.3, 21.4, R1.Pin_0
  N12: Bauteil1.D2_PWM, Switch.1, R3.Pin_0
  N13: Bauteil1.D3_PWM, Switch.2, R2.Pin_0
  N14: Bauteil1.D5_PWM, 5.anode
  N15: Bauteil1.D34, 330-R1.Pin_1
  N16: Bauteil1.D36, 330-R2.Pin_1
  N17: Bauteil1.D38, 330-R3.Pin_1
  N18: Bauteil1.D40, 330-R4.Pin_1
  N19: Bauteil1.D42, 330-R5.Pin_1
  N20: Bauteil1.D44, 330-R8.Pin_1
  N21: Bauteil1.D46, 330-R6.Pin_1
  N22: Bauteil1.D48, 330-R7.Pin_1
  N23: DI1.Segment_A#1, 330-R7.Pin_0
  N24: DI1.Segment_F, 330-R6.Pin_0
  N25: DI1.Segment_E, 330-R8.Pin_0
  N26: DI1.Segment_D, 330-R5.Pin_0
  N27: DI1.Segment_DP, 330-R4.Pin_0
  N28: DI1.Segment_C, 330-R3.Pin_0
  N29: DI1.Segment_B, 330-R2.Pin_0
  N30: DI1.Segment_A#10, 330-R1.Pin_0

notes:
  Data
  GND
  5V
  2
  3
  A8/62
  A9/63
