# Fritzing sketch id3134_Untitled_Sketch_0 (saved by Fritzing 0.9.3b)
breadboards: 1

parts:
  Parte1 = Arduino Leonardo (Rev3b)
  J1 = Basic Servo
  J2 = Basic Servo
  R1 = PHOTOCELL [package=photocell-kit]
  LED2 = RGB LED (com. cathode, rgb) [package="5 mm [THT]"]
  R2 = Resistor [tolerance=±5% resistance=220 package=THT]
  R3 = Resistor [tolerance=±5% resistance=220 package=THT]
  R4 = Resistor [tolerance=±5% resistance=220 package=THT]

nets:
  N1: Parte1.D7, R4.Pin_0
  VCC: Parte1.5V, J1.vcc, J2.vcc
  N2: Parte1.D8/A8, R3.Pin_0
  N3: Parte1.D9_PWM/A9, R2.Pin_0
  N4: Parte1.D10_PWM/A10, R1.P$1
  N5: Parte1.D11_PWM, J2.pulse
  N6: Parte1.D13_PWM, J1.pulse
  GND: Parte1.GND, J1.gnd, J2.gnd, R1.P$2, LED2.common_cathode
  N7: LED2.red_anode, R4.Pin_1
  N8: LED2.green_anode, R3.Pin_1
  N9: LED2.blue_anode, R2.Pin_1
