# Fritzing sketch id3135_Untitled_Sketch_0 (saved by Fritzing 0.9.3b)

parts:
  Relay_1_Channel = WeMos D1 Mini Relay Shield V2
  Vibration_Alarm_Sensor = Vibration Motor- ROB-08449 [package=vibe-motor-10mm]
  DC_to_DC_Step_down_LM2596 = prefix0000
  Buzzer = Piezo Speaker
  Arduino_UNO_R3 = Arduino Uno (Rev3)
  VCC4 = Battery block 9V  # not connected
  VCC3 = Battery block 9V
  Fuse = FUSE [package=fuse_5mm]
  IR_Receiver_Module_for_Remote_Control_Systems = TSOP312.., 314.. [package=THT]

nets:
  3V3: Relay_1_Channel.3V3, Arduino_UNO_R3.3V3
  N1: Relay_1_Channel.5V, Vibration_Alarm_Sensor.+, Buzzer.pin1
  N2: Relay_1_Channel.D8, Arduino_UNO_R3.D4
  N3: Relay_1_Channel.G, DC_to_DC_Step_down_LM2596.connector3
  N4: Relay_1_Channel.RX, Arduino_UNO_R3.D0/RX
  N5: Relay_1_Channel.TX, Arduino_UNO_R3.D1/TX
  N6: Vibration_Alarm_Sensor.-, Arduino_UNO_R3.D2
  N7: Buzzer.pin2, Arduino_UNO_R3.D3_PWM
  N8: Arduino_UNO_R3.D5_PWM, IR_Receiver_Module_for_Remote_Control_Systems.Data
  N9: Arduino_UNO_R3.5V, IR_Receiver_Module_for_Remote_Control_Systems.Vs
  GND: Arduino_UNO_R3.GND, IR_Receiver_Module_for_Remote_Control_Systems.GND
  N10: VCC3.+, Fuse.1
