# Fritzing sketch id3136_project_1__0 (saved by Fritzing 0.9.1b)
breadboards: 1

parts:
  Part1 = Arduino Uno (Rev3)
  LED1 = LED - 5mm [color="Red (635nm)" package="5 mm [THT]"]
  LED2 = LED - 5mm [color="Yellow (574nm)" package="5 mm [THT]"]
  LED3 = LED - 5mm [color="Green (570nm)" package="5 mm [THT]"]
  LED4 = LED - 5mm [color="Red (633nm)" package="5 mm [THT]"]
  LED5 = LED - 5mm [color="Yellow (595nm)" package="5 mm [THT]"]
  LED6 = LED - 5mm [color="Green (570nm)" package="5 mm [THT]"]
  R1 = Resistor [tolerance=±5% resistance=220 package=THT]
  R2 = Photocell (LDR) [package=THT]

nets:
  N1: Part1.D8, LED3.anode
  N2: Part1.D11_PWM/MOSI, LED4.cathode
  N3: Part1.D12/MISO, LED5.cathode
  N4: Part1.D13/SCK, LED6.cathode
  N5: Part1.D6_PWM, LED1.anode
  N6: Part1.GND, LED1.cathode, LED2.cathode, LED3.cathode, LED4.anode, LED5.anode, LED6.anode, R1.Pin_0
  N7: R1.Pin_1, R2.pin_0, R2.pin_1
