# Fritzing sketch id3137_Project_1_0 (saved by Fritzing 0.9.3b)
breadboards: 1

parts:
  Arduino = Arduino Uno (Rev3)
  PC1 = PHOTOCELL [package=photocell-kit]
  R5 = Resistor [tolerance=±5% resistance=10k package="0402 [SMD]"]
  PC3 = PHOTOCELL [package=photocell-kit]
  R4 = Resistor [tolerance=±5% resistance=10k package="0402 [SMD]"]
  PC2 = PHOTOCELL [package=photocell-kit]
  R3 = Resistor [tolerance=±5% resistance=10k package="0402 [SMD]"]
  PC4 = PHOTOCELL [package=photocell-kit]
  R2 = Resistor [tolerance=±5% resistance=10k package="0402 [SMD]"]
  PC5 = PHOTOCELL [package=photocell-kit]
  R1 = Resistor [tolerance=±5% resistance=10k package="0402 [SMD]"]
  D1 = Rectifier Diode [part_number=1N4001 package="300 mil [THT]"]
  D2 = Rectifier Diode [part_number=1N4001 package="300 mil [THT]"]
  D3 = Rectifier Diode [part_number=1N4001 package="300 mil [THT]"]
  D4 = Rectifier Diode [part_number=1N4001 package="300 mil [THT]"]
  D5 = Rectifier Diode [part_number=1N4001 package="300 mil [THT]"]
  Q2 = Basic FET P-Channel [package="TO220 [THT]"]
  Q3 = Basic FET P-Channel [package="TO220 [THT]"]
  Q4 = Basic FET P-Channel [package="TO220 [THT]"]
  Q5 = Basic FET P-Channel [package="TO220 [THT]"]
  Solenoid_5 = Solenoid
  Solenoid_3 = Solenoid
  Solenoid_1 = Solenoid
  R6 = Resistor [tolerance=±5% resistance=1k package="0603 [SMD]"]
  R7 = Resistor [tolerance=±5% resistance=1k package="0603 [SMD]"]
  R8 = Resistor [tolerance=±5% resistance=1k package="0603 [SMD]"]
  R9 = Resistor [tolerance=±5% resistance=1k package="0603 [SMD]"]
  R10 = Resistor [tolerance=±5% resistance=1k package="0603 [SMD]"]
  Q1 = Basic FET P-Channel [package="TO220 [THT]"]
  Solenoid_4 = Solenoid
  Solenoid_2 = Solenoid
  Laser_Diode_1 = LEDs [package=led10mm]
  Laser_Diode_2 = LEDs [package=led10mm]
  Laser_Diode_4 = LEDs [package=led10mm]
  Laser_Diode_5 = LEDs [package=led10mm]
  Laser_Diode_3 = LEDs [package=led10mm]

nets:
  N1: Arduino.A0, PC1.P$2, R1.Pin_0
  N2: Arduino.A1, PC2.P$2, R2.Pin_0
  N3: Arduino.A2, PC3.P$2, R3.Pin_0
  N4: Arduino.A3, R4.Pin_0, PC4.P$2
  N5: Arduino.D9_PWM, R9.Pin_0
  N6: Arduino.D10_PWM/SS, R10.Pin_0
  N7: Arduino.GND, R5.Pin_1, R4.Pin_1, R3.Pin_1, R2.Pin_1, R1.Pin_1, Q2.source, Q3.source, Q4.source, Q5.source, Q1.source, Laser_Diode_1.C, Laser_Diode_2.C, Laser_Diode_4.C, Laser_Diode_5.C, Laser_Diode_3.C
  N8: Arduino.A4/SDA, R5.Pin_0, PC5.P$2
  N9: Arduino.D3_PWM, R6.Pin_0
  N10: Arduino.D5_PWM, R7.Pin_0
  N11: Arduino.D6_PWM, R8.Pin_0
  N12: Arduino.5V, PC1.P$1, PC3.P$1, PC2.P$1, PC4.P$1, PC5.P$1, D1.cathode, D2.cathode, D3.cathode, D4.cathode, D5.cathode, Solenoid_5.pin1, Solenoid_3.pin1, Solenoid_1.pin1, Solenoid_4.pin1, Solenoid_2.pin1, Laser_Diode_1.A, Laser_Diode_2.A, Laser_Diode_4.A, Laser_Diode_5.A, Laser_Diode_3.A
  N13: D1.anode, Solenoid_5.pin2, Q1.gate
  N14: D2.anode, Q2.gate, Solenoid_4.pin2
  N15: D3.anode, Q3.gate, Solenoid_3.pin2
  N16: D4.anode, Q4.gate, Solenoid_2.pin2
  N17: D5.anode, Q5.gate, Solenoid_1.pin2
  N18: Q2.drain, R7.Pin_1
  N19: Q3.drain, R8.Pin_1
  N20: Q4.drain, R9.Pin_1
  N21: Q5.drain, R10.Pin_1
  N22: R6.Pin_1, Q1.drain
