# Fritzing sketch id3138_Arduino_+_Tiny's_2_0 (saved by Fritzing 0.9.3b)
circuit board: 8.46667cm x 5.64444cm
breadboards: 1

parts:
  R1 = Resistor [tolerance=±5% resistance=10k package=THT]
  LM555 = 555 Timer [package="DIP8 [THT]"]
  R2 = Resistor [tolerance=±5% resistance=68k package=THT]
  R3 = 250 kohm
  C1_(10µF) = Capacitor Polarized [package=panasonic_c]
  C2_(10nF) = Capacitor [package=cap-pth-small-kit]
  R4 = Resistor [tolerance=±5% resistance=10k package=THT]
  Arduino_UNO_(Rev3) = Arduino Uno (Rev3) - ICSP
  V3 = DC Power [voltage=5]
  R5 = Resistor [tolerance=±5% resistance=10k package=THT]
  Tiny1 = attiny85 [package=dip]
  Tiny2 = attiny85 [package=dip]
  Preset_1 = Pushbutton [package=THT]
  Preset2 = Pushbutton [package=THT]
  Preset3 = Pushbutton [package=THT]
  R8 = Resistor [tolerance=±5% resistance=220 package=THT]
  R9 = Resistor [tolerance=±5% resistance=1k package=THT]
  R10 = Resistor [tolerance=±5% resistance=10k package=THT]
  LM358AN = LM 358 Dual Op-Amp [package="DIP8 [THT]"]
  AC_Sensor = ACS712 [package=so08]
  R11 = Resistor [tolerance=±5% resistance=10k package=THT]
  R12 = Resistor [tolerance=±5% resistance=10k package=THT]
  R14 = Resistor [tolerance=±5% resistance=10k package=THT]
  R15 = Rotary Potentiometer (Large) [maximum_resistance=10kΩ package=THT]
  R16 = Resistor [tolerance=±5% resistance=47k package=THT]
  1n4148 = Diode [package=diode-1n4148]
  R17 = Resistor [tolerance=±5% resistance=4.7k package=THT]
  C3_(0_1µF) = Capacitor Polarized [package=panasonic_c]
  R18 = Resistor [tolerance=±5% resistance=10k package=THT]
  R19 = Resistor [tolerance=±5% resistance=68k package=THT]
  LM556 = 555 Timer [package="DIP8 [THT]"]
  R20 = 250 kohm
  C1_(10µF)1 = Capacitor Polarized [package=panasonic_c]
  C2_(10nF)1 = Capacitor [package=cap-pth-small-kit]
  Tiny3 = attiny85 [package=dip]
  C3_(0_1µF)1 = Capacitor Polarized [package=panasonic_c]
  Tiny4 = attiny85 [package=dip]
  LM358AN1 = LM 358 Dual Op-Amp [package="DIP8 [THT]"]
  AC_Sensor1 = ACS712 [package=so08]
  R21 = Resistor [tolerance=±5% resistance=10k package=THT]
  R22 = Resistor [tolerance=±5% resistance=10k package=THT]
  R23 = Resistor [tolerance=±5% resistance=10k package=THT]
  R24 = Rotary Potentiometer (Large) [maximum_resistance=10kΩ package=THT]
  1n4149 = Diode [package=diode-1n4148]
  R25 = Resistor [tolerance=±5% resistance=4.7k package=THT]
  V4 = DC Power [voltage=5]

nets:
  N1: R1.Pin_0, LM555.Discharge, R2.Pin_1
  N2: R1.Pin_1, LM555.Reset, LM555.Vcc_Supply_Voltage, R4.Pin_0, V3.V+, R5.Pin_0, Tiny1.Pin_8, Tiny2.Pin_8, Preset_1.leg1, Preset2.leg1, Preset3.leg1, LM358AN.connector7, AC_Sensor.VCC, R15.leg2, R18.Pin_1, LM556.Reset, LM556.Vcc_Supply_Voltage, Tiny3.Pin_8
  GND: LM555.Ground, R3.connector0, C1_(10µF).-, C2_(10nF).2, Arduino_UNO_(Rev3).GND, V3.V-, Tiny1.Pin_4, Tiny2.Pin_4, R8.Pin_0, R9.Pin_0, R10.Pin_0, LM358AN.connector3, AC_Sensor.GND, R12.Pin_0, R15.leg1, R17.Pin_0, C3_(0_1µF).-, LM556.Ground, R20.connector0, C1_(10µF)1.-, C2_(10nF)1.2, Tiny3.Pin_4, C3_(0_1µF)1.-, Tiny4.Pin_4, LM358AN1.connector3, AC_Sensor1.GND, R22.Pin_0, R24.leg1, R25.Pin_0, V4.V-
  N3: LM555.Trigger, LM555.Threshold, R3.connector1, C1_(10µF).+
  N4: LM555.Output, Tiny1.Pin_6, Preset_1.leg0, Preset2.leg0, Preset3.leg0, R8.Pin_1, R9.Pin_1, R10.Pin_1
  N5: LM555.Control_Voltage, C2_(10nF).1
  N6: R2.Pin_0, R3.connector2
  N7: R4.Pin_1, Arduino_UNO_(Rev3).A4/SDA, Tiny3.Pin_5
  N8: Arduino_UNO_(Rev3).A5/SCL, R5.Pin_1, Tiny1.Pin_7, Tiny2.Pin_7, Tiny3.Pin_7, Tiny4.Pin_7
  N9: Arduino_UNO_(Rev3).ICSP_MISO, Arduino_UNO_(Rev3).D12/MISO, Tiny1.Pin_5, Tiny2.Pin_5, Tiny4.Pin_5
  5V: Arduino_UNO_(Rev3).5V, Tiny4.Pin_8, LM358AN1.connector7, AC_Sensor1.VCC, R24.leg2, V4.V+
  N10: Tiny2.Pin_6, 1n4148.C, R17.Pin_1, C3_(0_1µF).+
  N11: LM358AN.connector0, R16.Pin_1, 1n4148.A
  N12: LM358AN.connector1, R14.Pin_1, R16.Pin_0
  N13: LM358AN.connector2, R11.Pin_1, R12.Pin_1
  N14: AC_Sensor.VOUT, R11.Pin_0
  N15: R14.Pin_0, R15.wiper
  N16: R18.Pin_0, R19.Pin_1, LM556.Discharge
  N17: R19.Pin_0, R20.connector2
  N18: LM556.Trigger, LM556.Threshold, R20.connector1, C1_(10µF)1.+
  N19: LM556.Output, Tiny3.Pin_6
  N20: LM556.Control_Voltage, C2_(10nF)1.1
  N21: C3_(0_1µF)1.+, Tiny4.Pin_6, 1n4149.C, R25.Pin_1
  N22: LM358AN1.connector0, 1n4149.A
  N23: LM358AN1.connector1, R23.Pin_1
  N24: LM358AN1.connector2, R21.Pin_1, R22.Pin_1
  N25: AC_Sensor1.VOUT, R21.Pin_0
  N26: R23.Pin_0, R24.wiper
