# Fritzing sketch id3138_numeric_keypad (saved by Fritzing 0.3.14b)
breadboards: 3

parts:
  DI1 = 7-Segment LED Display [package=THT]
  R1 = Resistor [resistance=220 package=THT]
  R2 = Resistor [resistance=220 package=THT]
  R3 = Resistor [resistance=220 package=THT]
  R4 = Resistor [resistance=220 package=THT]
  R6 = Resistor [resistance=220 package=THT]
  R7 = Resistor [resistance=220 package=THT]
  R8 = Resistor [resistance=1.5k package=THT]
  R9 = Resistor [resistance=220 package=THT]
  VCC1 = obsolete Battery
  1 = Pushbutton [package=THT]
  2 = Pushbutton [package=THT]
  3 = Pushbutton [package=THT]
  4 = Pushbutton [package=THT]
  5 = Pushbutton [package=THT]
  6 = Pushbutton [package=THT]
  7 = Pushbutton [package=THT]
  8 = Pushbutton [package=THT]
  9 = Pushbutton [package=THT]
  0 = Pushbutton [package=THT]
  DP_S = Pushbutton [package=THT]

nets:
  N1: DI1.cathodeE, R6.Pin_1
  N2: DI1.cathodeD, R9.Pin_1
  N3: DI1.commAnode, VCC1.-
  N4: DI1.cathodeC, R7.Pin_0
  N5: DI1.cathodeDP, R8.Pin_0
  N6: DI1.cathodeB, R1.Pin_0
  N7: DI1.cathodeA, R2.Pin_0
  N8: DI1.cathodeF, R3.Pin_1
  N9: DI1.cathodeG, R4.Pin_1
  N10: R1.Pin_1, R2.Pin_1, R3.Pin_0, R4.Pin_0, R6.Pin_0, R7.Pin_1, R9.Pin_0, 1.leg0, 2.leg0, 3.leg0, 4.leg0, 5.leg0, 6.leg0, 7.leg0, 8.leg0, 9.leg0, 0.leg0
  N11: R8.Pin_1, DP_S.leg0
  N12: VCC1.+, 1.leg1, 2.leg1, 3.leg1, 4.leg1, 5.leg1, 6.leg1, 7.leg1, 8.leg1, 9.leg1, 0.leg1, DP_S.leg1
