# Fritzing sketch id3139_fritzig_0 (saved by Fritzing 0.9.2b)
perfboards: 3

parts:
  VCC1 = Battery
  LED1 = LED - 5mm [color="Red (633nm)" package="5 mm [THT]"]
  LED2 = Super Flux LED blue [color=Blue]
  LED3 = LED - 5mm [color="Red (633nm)" package="5 mm [THT]"]
  LED4 = Super Flux LED blue [color=Blue]
  LED5 = LED - 5mm [color="Red (633nm)" package="5 mm [THT]"]
  LED6 = Super Flux LED blue [color=Blue]
  LED7 = LED - 5mm [color="Red (633nm)" package="5 mm [THT]"]
  LED8 = Super Flux LED blue [color=Blue]
  LED9 = LED - 5mm [color="Red (633nm)" package="5 mm [THT]"]
  LED10 = Super Flux LED blue [color=Blue]
  LED11 = LED - 5mm [color="Red (633nm)" package="5 mm [THT]"]
  LED12 = Super Flux LED blue [color=Blue]
  LED13 = LED - 5mm [color="Red (633nm)" package="5 mm [THT]"]
  LED14 = Super Flux LED blue [color=Blue]
  LED15 = LED - 5mm [color="Red (633nm)" package="5 mm [THT]"]
  LED16 = Super Flux LED blue [color=Blue]
  LED17 = LED - 5mm [color="Red (633nm)" package="5 mm [THT]"]
  LED18 = Super Flux LED blue [color=Blue]
  LED19 = LED - 5mm [color="Red (633nm)" package="5 mm [THT]"]
  LED20 = Super Flux LED blue [color=Blue]
  LED21 = LED - 5mm [color="Red (633nm)" package="5 mm [THT]"]
  Part1 = Arduino Uno (Rev3)
  SPKR1 = Loudspeaker
  LED22 = LED - 5mm [color="Red (633nm)" package="5 mm [THT]"]  # not connected
  LED23 = LED - 5mm [color="Red (633nm)" package="5 mm [THT]"]  # not connected
  LED24 = LED - 5mm [color="Red (633nm)" package="5 mm [THT]"]  # not connected
  LED25 = LED - 5mm [color="Red (633nm)" package="5 mm [THT]"]  # not connected
  VCC2 = Battery
  S1 = Pushbutton [package=THT]
  R1 = Resistor [tolerance=±5% resistance=220 package=THT]  # not connected
  R2 = Resistor [tolerance=±5% resistance=220 package=THT]  # not connected
  R3 = Resistor [tolerance=±5% resistance=220 package=THT]  # not connected
  R4 = Resistor [tolerance=±5% resistance=220 package=THT]  # not connected
  EDGY_motor_control1 = EDGY
  VCC3 = Battery
  M1 = DC Motor
  S2 = Round Pushbutton

nets:
  N1: VCC1.-, LED21.cathode, S1.leg0
  N2: VCC1.+, LED1.cathode, S1.leg1
  N3: LED2.anode, LED2.cathode
  N4: LED3.anode, LED4.anode, LED4.cathode
  N5: LED5.anode, LED6.anode, LED6.cathode
  N6: LED7.anode, LED8.anode, LED8.cathode, LED9.cathode
  N7: LED9.anode, LED10.anode, LED10.cathode, LED11.cathode
  N8: LED11.anode, LED12.anode, LED12.cathode, LED13.anode
  N9: LED13.cathode, LED14.anode, LED14.cathode, LED15.anode
  N10: LED15.cathode, LED16.anode, LED16.cathode, LED17.anode
  N11: LED17.cathode, LED18.anode, LED18.cathode, LED19.anode
  N12: LED19.cathode, LED20.anode, LED20.cathode, LED21.anode
  N13: Part1.A4/SDA, SPKR1.pin1
  N14: Part1.A5/SCL, SPKR1.pin2
  N15: Part1.GND, VCC2.+
  N16: Part1.VIN, VCC2.-
  N17: EDGY_motor_control1.B1out, M1.pin_2
  N18: EDGY_motor_control1.A1out, M1.pin_1
  N19: VCC3.+, S2.leg0
