# Fritzing sketch id313_ampelDisco_0 (saved by Fritzing 0.9.2b)
breadboards: 2

parts:
  Kontroll-LED = LED - 5mm [color="Red (633nm)" package="5 mm [THT]"]
  LEDBlau = LED - 5mm [color="Blue (470nm)" package="5 mm [THT]"]
  LEDGruen = LED - 5mm [color="Green (560nm)" package="5 mm [THT]"]
  Regler = Rotary Potentiometer (Small) [maximum_resistance=100kΩ package=THT]
  R2 = Resistor [tolerance=±5% resistance=220 package=THT]
  R3 = Resistor [tolerance=±5% resistance=220 package=THT]
  ampelDisco = Arduino Uno (Rev3)

nets:
  N1: Kontroll-LED.cathode, LEDBlau.cathode, LEDGruen.cathode, Regler.leg1, ampelDisco.GND
  N2: Kontroll-LED.anode, Regler.wiper, ampelDisco.A0
  N3: LEDBlau.anode, R3.Pin_1
  N4: LEDGruen.anode, R2.Pin_1
  N5: Regler.leg2, ampelDisco.5V
  N6: R2.Pin_0, ampelDisco.D2
  N7: R3.Pin_0, ampelDisco.D4
