# Fritzing sketch id3141_Project_3_0 (saved by Fritzing 0.9.2b)
breadboards: 1

parts:
  Part1 = Arduino Uno (Rev3)
  R1 = Rotary Potentiometer (Small) [maximum_resistance=100kΩ package=THT]
  R2 = Slide Potentiometer [maximum_resistance=100kΩ]
  R3 = Resistor [tolerance=±5% resistance=220 package=THT]  # not connected
  LED1 = LED - 5mm [color="Red (633nm)" package="5 mm [THT]"]
  LED2 = LED - 5mm [color="Red (633nm)" package="5 mm [THT]"]
  LED3 = LED - 5mm [color="Red (633nm)" package="5 mm [THT]"]
  R4 = Resistor [tolerance=±5% resistance=220 package=THT]
  R5 = Resistor [tolerance=±5% resistance=220 package=THT]
  R6 = Resistor [tolerance=±5% resistance=220 package=THT]
  LED4 = RGB LED (com. cathode, rgb) [package="5 mm [THT]"]
  R7 = Resistor [tolerance=±5% resistance=220 package=THT]
  R8 = Resistor [tolerance=±5% resistance=220 package=THT]
  R9 = Resistor [tolerance=±5% resistance=220 package=THT]

nets:
  N1: Part1.A0, R2.leg2
  N2: Part1.A5/SCL, R1.wiper
  N3: Part1.D8, R9.Pin_1
  N4: Part1.D9_PWM, R7.Pin_0
  N5: Part1.D10_PWM/SS, R8.Pin_1
  N6: Part1.D2, R6.Pin_0
  N7: Part1.D3_PWM, R5.Pin_1
  N8: Part1.D4, R4.Pin_1
  N9: Part1.5V, R1.leg2
  N10: Part1.GND, R1.leg1, R2.leg1, LED1.cathode, LED2.cathode, LED3.cathode
  N11: LED1.anode, R4.Pin_0
  N12: LED2.anode, R5.Pin_0
  N13: LED3.anode, R6.Pin_1
  N14: LED4.red_anode, R9.Pin_0
  N15: LED4.green_anode, R8.Pin_0
  N16: LED4.blue_anode, R7.Pin_1
