# Fritzing sketch id3142_MyProject3Schematic_0 (saved by Fritzing 0.9.3b)
breadboards: 1

parts:
  Q1 = NPN-Transistor [package="TO92 [THT]"]
  LED1 = LED - 5mm [color="Red (633nm)" package="5 mm [THT]"]
  Part1 = Arduino Mega 2560 (Rev3)
  P1 = S1133 Si Photodiode [package="8mm Ceramic [THT]"]
  4_7k_resistor = Resistor [tolerance=±5% resistance=220 package="0402 [SMD]"]
  4_7k_resistor_2 = Resistor [tolerance=±5% resistance=220 package="0402 [SMD]"]

nets:
  N1: Q1.E, LED1.cathode, Part1.GND, 4_7k_resistor.Pin_0
  N2: Q1.B, P1.anode, 4_7k_resistor.Pin_1
  N3: Q1.C, LED1.anode, Part1.D19/RX1, 4_7k_resistor_2.Pin_0
  N4: Part1.5V, P1.cathode, 4_7k_resistor_2.Pin_1
