# Fritzing sketch id3143_Project_1_unesp_0 (saved by Fritzing 0.9.3b)
breadboards: 1

parts:
  M1 = Stepper Motor - Bipolar  # not connected
  J1 = Basic Servo
  Part1 = Arduino Uno (Rev3) - ICSP

nets:
  GND: J1.gnd, Part1.GND
  VCC: J1.vcc, Part1.5V
  N1: J1.pulse, Part1.D3_PWM
