# Fritzing sketch id3144_Project_Tas_SKetch_0 (saved by Fritzing 0.9.3b)
breadboards: 1

parts:
  J1 = Basic Servo
  Onderdeel1 = Arduino Uno (Rev3)
  S1 = Pushbutton [package="[THT]"]
  J2 = Basic Force Sensing Resistor (FSR) [package=THT]
  R1 = Resistor [tolerance=±5% resistance=10k package="2010 [SMD]"]
  R2 = Resistor [tolerance=±5% resistance=1k package="2010 [SMD]"]

nets:
  GND: J1.gnd, Onderdeel1.GND, R1.Pin_1, R2.Pin_1
  N1: J1.pulse, Onderdeel1.D9_PWM
  N2: Onderdeel1.A0, J2.pin_1, R2.Pin_0
  N3: Onderdeel1.5V, S1.Pin_3, S1.Pin_4
  N4: S1.Pin_1, S1.Pin_2, R1.Pin_0
