# Fritzing sketch id3145_Project_Whurl_Sketch_0 (saved by Fritzing 0.9.3b)

parts:
  Part1 = Arduino Mega 2560 (Rev3)
  MicroSD_Module = MicroSD Card Module
  3-axis_Accelerometer = Grove 3 Axis Digital Accelerometer 16g
  Arduion_Mega_with_GSM_Shield = Arduino GSM Shield

nets:
  N1: Part1.A0, Arduion_Mega_with_GSM_Shield.A0
  N2: Part1.A1, Arduion_Mega_with_GSM_Shield.A1
  N3: Part1.A2, Arduion_Mega_with_GSM_Shield.A2
  N4: Part1.A3, Arduion_Mega_with_GSM_Shield.A3
  N5: Part1.A4, Part1.D20/SDA, Part1.SDA, 3-axis_Accelerometer.SDA, Arduion_Mega_with_GSM_Shield.A4/SDA
  N6: Part1.A5, Part1.D21/SCL, Part1.SCL, 3-axis_Accelerometer.SCL, Arduion_Mega_with_GSM_Shield.A5/SCL
  N7: Part1.AREF, Arduion_Mega_with_GSM_Shield.AREF
  GND: Part1.GND, MicroSD_Module.GND, 3-axis_Accelerometer.GND, Arduion_Mega_with_GSM_Shield.AGND
  N8: Part1.D13_PWM, Arduion_Mega_with_GSM_Shield.SCK/D13
  N9: Part1.D12_PWM, Arduion_Mega_with_GSM_Shield.MISO/D12
  N10: Part1.D11_PWM, Arduion_Mega_with_GSM_Shield.MOSI/PWM_D11
  N11: Part1.D10_PWM, Arduion_Mega_with_GSM_Shield.SS/PWM_D10
  N12: Part1.D9_PWM, Arduion_Mega_with_GSM_Shield.PWM_D9
  N13: Part1.D8_PWM, Arduion_Mega_with_GSM_Shield.D8
  N14: Part1.IOREF#254, Arduion_Mega_with_GSM_Shield.N/C
  N15: Part1.IOREF#255, Arduion_Mega_with_GSM_Shield.IOREF
  N16: Part1.RESET, Arduion_Mega_with_GSM_Shield.RST_ARDUINO
  3V3: Part1.3V3, 3-axis_Accelerometer.VCC, Arduion_Mega_with_GSM_Shield.3V3
  5V: Part1.5V, MicroSD_Module.VCC, Arduion_Mega_with_GSM_Shield.5V
  VIN: Part1.VIN, Arduion_Mega_with_GSM_Shield.VIN
  N17: Part1.D0_RX0, Arduion_Mega_with_GSM_Shield.N/C_D0
  N18: Part1.D1_TX0, Arduion_Mega_with_GSM_Shield.N/C_D1
  N19: Part1.D2_PWM, Arduion_Mega_with_GSM_Shield.DSM_RX_D2
  N20: Part1.D3_PWM, Arduion_Mega_with_GSM_Shield.DSM_TX_D3
  N21: Part1.D4_PWM, Arduion_Mega_with_GSM_Shield.PWM_D4
  N22: Part1.D5_PWM, Arduion_Mega_with_GSM_Shield.PWM_D5
  N23: Part1.D6_PWM, Arduion_Mega_with_GSM_Shield.PWM_D6
  N24: Part1.D7_PWM, Arduion_Mega_with_GSM_Shield.RST_MDM/D7
  N25: Part1.D50, MicroSD_Module.MISO
  N26: Part1.D51, MicroSD_Module.MOSI
  N27: Part1.D52, MicroSD_Module.SCK
  N28: Part1.D53, MicroSD_Module.CS
