# Fritzing sketch id3146_Object_Avoiding_Vehicle (saved by Fritzing 0.6.5b)
breadboards: 1

parts:
  VCC1 = Battery
  IC1 = PICAXE-18M [package=THT]
  R1 = Resistor [tolerance=±5% resistance=390 package=THT]
  LED1 = LED - 5mm [color="Infrared (940nm)" package="5 mm [THT]"]
  LED2 = LED - 5mm [color="White (8000K)" package="5 mm [THT]"]
  R2 = Resistor [tolerance=±5% resistance=1k package=THT]
  R3 = Resistor [tolerance=±5% resistance=10k package=THT]
  LED3 = LED - 5mm [color="Infrared (940nm)" package="5 mm [THT]"]
  LED4 = LED - 5mm [color="White (8000K)" package="5 mm [THT]"]
  R4 = Resistor [tolerance=±5% resistance=390 package=THT]
  R5 = Resistor [tolerance=±5% resistance=1k package=THT]
  R6 = Resistor [tolerance=±5% resistance=1k package=THT]
  Q2 = NPN-Transistor [package="TO92 [THT]"]
  Q3 = NPN-Transistor [package="TO92 [THT]"]
  M1 = DC Motor
  M2 = DC Motor
  R7 = Resistor [tolerance=±5% resistance=1k package=THT]
  R8 = Resistor [tolerance=±5% resistance=10k package=THT]
  LED5 = LED - 5mm [color="Red (633nm)" package="5 mm [THT]"]
  R9 = Resistor [tolerance=±5% resistance=150 package=THT]
  R10 = Resistor [tolerance=±5% resistance=220 package=THT]
  LED6 = LED - 5mm [color="Red (633nm)" package="5 mm [THT]"]
  S1 = Pushbutton [package=THT]
  LED7 = LED - 5mm [color="Red (633nm)" package="5 mm [THT]"]
  R11 = Resistor [tolerance=±5% resistance=150 package=THT]
  R12 = Resistor [tolerance=±5% resistance=150 package=THT]
  LED8 = LED - 5mm [color="Red (633nm)" package="5 mm [THT]"]

nets:
  N1: VCC1.-, LED1.cathode, R3.Pin_0, Q2.C, Q3.E, R8.Pin_0, LED5.cathode, R9.Pin_0, R10.Pin_0, LED6.cathode, LED7.cathode
  N2: VCC1.+, R1.Pin_1, LED2.anode, LED4.anode, R4.Pin_1, M1.pin_2, M2.pin_2, S1.leg1
  N3: IC1.0V, LED3.cathode, LED8.cathode
  N4: IC1.Out_1, R5.Pin_0
  N5: IC1.Out_2, R6.Pin_0
  N6: IC1.+V, S1.leg0
  N7: IC1.In_0_/_ADC_0_/_Infrain, R7.Pin_1
  N8: IC1.In_1_/_ADC_1, R2.Pin_1
  N9: R1.Pin_0, LED1.anode
  N10: LED2.cathode, R2.Pin_0, R3.Pin_1, R11.Pin_0
  N11: LED3.anode, R4.Pin_0
  N12: LED4.cathode, R7.Pin_0, R8.Pin_1, R12.Pin_1
  N13: R5.Pin_1, Q3.B
  N14: R6.Pin_1, Q2.B
  N15: Q2.E, M2.pin_1
  N16: Q3.C, M1.pin_1
  N17: LED5.anode, R9.Pin_1
  N18: R10.Pin_1, LED6.anode
  N19: LED7.anode, R11.Pin_1
  N20: R12.Pin_0, LED8.anode
