# Fritzing sketch id3146_Untitled_Sketch_2_0 (saved by Fritzing 0.9.2b)

parts:
  Part1 = Arduino Mega 2560 (Rev3)
  Part2 = Arduino Leonardo (Rev3b)
  U1 = LIPO-2000mAh [package=lipo-2000]
  S4 = SWITCH-MOMENTARY-2 [package=tactile_switch_smd-2]
  J1 = Infrared Proximity Sensor
  J2 = Infrared Proximity Sensor
  J3 = Infrared Proximity Sensor
  J4 = Basic Servo

nets:
  N1: Part1.A1, J1.Vout
  N2: Part1.A2, J2.Vout
  N3: Part1.A3, J3.Vout
  VCC: Part1.5V, J1.Vcc, J2.Vcc, J3.Vcc
  GND: Part1.GND, J1.GND, J2.GND, J3.GND
  5V: Part2.5V, J4.vcc
  GND_2: Part2.GND, J4.gnd
  N4: Part2.D8/A8, J4.pulse
  N5: U1.+, S4.1

notes:
  Ultra Sonic Sensor "Front"
  Ultra Sonic Sensor "side"
  ESC
