# Fritzing sketch id3147_rgb_led_0 (saved by Fritzing 0.8.5b)
breadboards: 1

parts:
  Part1 = Arduino Uno (Rev3)
  R1 = Rotary Potentiometer (Small) [maximum_resistance=100kΩ package=THT]
  R2 = Rotary Potentiometer (Small) [maximum_resistance=100kΩ package=THT]  # not connected
  R3 = Rotary Potentiometer (Small) [maximum_resistance=100kΩ package=THT]
  R4 = Resistor [tolerance=±5% resistance=200 package=THT]
  R5 = Resistor [tolerance=±5% resistance=120 package=THT]
  R6 = Resistor [tolerance=±5% resistance=120 package=THT]
  LED1 = RGB LED (com. cathode, rbg) [package="5 mm [THT]"]

nets:
  N1: Part1.A0, R1.wiper
  N2: Part1.A1, R3.wiper
  N3: Part1.D3_PWM, R6.Pin_0
  N4: Part1.D5_PWM, R5.Pin_0
  N5: Part1.D6_PWM, R4.Pin_0
  N6: Part1.5V, R1.leg2, R3.leg2
  N7: Part1.GND, R1.leg1, R3.leg1, LED1.common_cathode
  N8: R5.Pin_1, LED1.blue_anode
  N9: R6.Pin_1, LED1.green_anode
