# Fritzing sketch id3149_arduino_ldc_temperatura_luminozidade_0 (saved by Fritzing 0.7.12b)
breadboards: 1

parts:
  Arduino1 = Arduino
  LCD1 = LCD screen
  R1 = Rotary Potentiometer (Large) [maximum_resistance=100kΩ package=THT]
  R2 = Rotary Potentiometer (Large) [maximum_resistance=100kΩ package=THT]
  R3 = Photocell (LDR) [package=THT]
  T1 = LM35 Temperature Sensor [package="TO92 [THT]"]
  R4 = Resistor [tolerance=±5% resistance=10k package=THT]

nets:
  N1: Arduino1.D9, LCD1.RS
  N2: Arduino1.D8, LCD1.E
  N3: Arduino1.D5, LCD1.DB4
  N4: Arduino1.D4, LCD1.DB5
  N5: Arduino1.D3, LCD1.DB6
  N6: Arduino1.D2, LCD1.DB7
  +5V: Arduino1.+5V, LCD1.VDD, R1.leg1, R2.leg1, R3.pin_0, T1.+Vs
  GND: Arduino1.GND, LCD1.VSS, LCD1.R/W, LCD1.LED-, R1.leg2, R2.leg2, T1.GND, R4.Pin_0
  N7: Arduino1.A0, R3.pin_1, R4.Pin_1
  N8: Arduino1.A1, T1.Vout
  N9: LCD1.V0, R1.wiper
  N10: LCD1.LED+, R2.wiper
