# Fritzing sketch id314_Ampelsteuerung_1_0 (saved by Fritzing 0.8.3b)
circuit board: 16.9333cm x 5.64444cm
breadboards: 3

parts:
  LED1 = LED - 5mm [color="Red (633nm)" current=20mA package="5 mm [THT]"]
  LED2 = LED - 5mm [color="Yellow (595nm)" package="5 mm [THT]"]
  LED3 = LED - 5mm [color="Green (555nm)" package="5 mm [THT]"]
  R1 = Resistor [tolerance=±20% resistance=2.2k power=250mW part_number=R1 package=THT]
  R2 = Resistor [tolerance=±20% resistance=2.2k part_number=R2 package=THT]
  R3 = Resistor [tolerance=±20% resistance=2.2k part_number=R3 package=THT]
  LED4 = LED - 5mm [color="Red (633nm)" current=20mA package="5 mm [THT]"]
  LED5 = LED - 5mm [color="Yellow (595nm)" package="5 mm [THT]"]
  LED6 = LED - 5mm [color="Green (555nm)" package="5 mm [THT]"]
  LED7 = LED - 5mm [color="Red (633nm)" current=20mA package="5 mm [THT]"]
  LED8 = LED - 5mm [color="Green (555nm)" package="5 mm [THT]"]
  LED9 = LED - 5mm [color="Red (633nm)" current=20mA package="5 mm [THT]"]
  LED10 = LED - 5mm [color="Green (555nm)" package="5 mm [THT]"]
  R4 = Resistor [tolerance=±20% resistance=2.2k part_number=R4 package=THT]
  R5 = Resistor [tolerance=±20% resistance=2.2k part_number=R5 package=THT]
  R6 = Resistor [tolerance=±20% resistance=2.2k part_number=R6 package=THT]
  R7 = Resistor [tolerance=±20% resistance=2.2k part_number=R7 package=THT]
  R8 = Resistor [tolerance=±20% resistance=2.2k part_number=R8 package=THT]
  R9 = Resistor [tolerance=±20% resistance=2.2k part_number=R9 package=THT]
  R10 = Resistor [tolerance=±20% resistance=2.2k part_number=R10 package=THT]
  S1 = Pushbutton [package="[THT]"]
  S2 = Pushbutton [package="[THT]"]
  C2 = Ceramic Capacitor [capacitance=100nF package="100 mil [THT, multilayer]"]
  C3 = Ceramic Capacitor [capacitance=100nF package="100 mil [THT, multilayer]"]
  Bauteil1 = Arduino Uno (Rev3)

nets:
  N1: LED1.cathode, R1.Pin_0, LED6.cathode, R7.Pin_0
  N2: LED1.anode, LED2.anode, LED3.anode, LED4.anode, LED5.anode, LED6.anode, LED7.anode, LED8.anode, LED9.anode, LED10.anode, S1.Pin_3, S1.Pin_4, S2.Pin_3, S2.Pin_4, C2.0, C3.0, Bauteil1.GND
  N3: LED2.cathode, R6.Pin_0
  N4: LED3.cathode, R5.Pin_0
  N5: R1.Pin_1, Bauteil1.ICSP_SCK, Bauteil1.D13/SCK
  N6: R2.Pin_0, LED9.cathode
  N7: R2.Pin_1, Bauteil1.ICSP_MISO, Bauteil1.D12/MISO
  N8: R3.Pin_0, LED10.cathode
  N9: R3.Pin_1, Bauteil1.ICSP_MOSI, Bauteil1.D11_PWM/MOSI
  N10: LED4.cathode, R10.Pin_0
  N11: LED5.cathode, R9.Pin_0
  N12: LED7.cathode, R4.Pin_0
  N13: LED8.cathode, R8.Pin_0
  N14: R4.Pin_1, Bauteil1.D10_PWM/SS
  N15: R5.Pin_1, Bauteil1.D9_PWM
  N16: R6.Pin_1, Bauteil1.D8
  N17: R7.Pin_1, Bauteil1.D7
  N18: R8.Pin_1, Bauteil1.D6_PWM
  N19: R9.Pin_1, Bauteil1.D5_PWM
  N20: R10.Pin_1, Bauteil1.D4
  N21: S1.Pin_1, S1.Pin_2, C3.1, Bauteil1.D3_PWM
  N22: S2.Pin_1, S2.Pin_2, C2.1, Bauteil1.D2

notes:
  Fußgänger 1
  Fußgänger 2
  Verkehr 1
  Verkehr 2
  Fußgängertaster 1
  Fußgängertaster 2
