# Fritzing sketch id3150_Arduino_e_sensor_LDR_0 (saved by Fritzing 0.7.10b)
breadboards: 1

parts:
  R1 = Photocell (LDR) [package=THT]
  R2 = Resistor [tolerance=±5% resistance=10k package=THT]
  LED1 = LED - 5mm [color="Red (633nm)" package="5 mm [THT]"]
  LED2 = LED - 5mm [color="Yellow (585nm)" package="5 mm [THT]"]
  LED3 = LED - 5mm [color="Green (555nm)" package="5 mm [THT]"]
  R3 = Resistor [tolerance=±5% resistance=100 package=THT]
  R4 = Resistor [tolerance=±5% resistance=100 package=THT]
  R5 = Resistor [tolerance=±5% resistance=100 package=THT]
  Arduino1 = Arduino

nets:
  N1: R1.pin_1, Arduino1.+5V
  N2: R2.Pin_0, LED1.cathode, LED2.cathode, LED3.cathode, Arduino1.GND
  N3: R2.Pin_1, Arduino1.A0
  N4: LED1.anode, R3.Pin_0, R3.Pin_1, Arduino1.D10
  N5: LED2.anode, R4.Pin_0, R4.Pin_1, Arduino1.D9
  N6: LED3.anode, R5.Pin_0, R5.Pin_1, Arduino1.D8
