# Fritzing sketch id3151_detectorDeLimpeza_0 (saved by Fritzing 0.9.2b)
circuit board: 6.88566cm x 5.36311cm
breadboards: 1

parts:
  S2 = Pushbutton [package="[THT]"]
  S3 = Pushbutton [package="[THT]"]
  S4 = Pushbutton [package="[THT]"]
  R4 = Resistor [tolerance=±5% resistance=10k package=THT]
  R5 = Resistor [tolerance=±5% resistance=10k package=THT]
  R6 = Resistor [tolerance=±5% resistance=10k package=THT]
  S1 = Pushbutton [package="[THT]"]
  J8 = double row female pin header, 14 pins [form="♀ (female)"]
  U1 = BNC [package=bnc]
  pH_Circuit1 = pH Circuit
  R7 = Resistor [tolerance=±5% resistance=10k package=THT]
  Часть1 = Arduino Uno (Rev3)
  LCD1 = LCD screen
  T1 = LM35 Temperature Sensor [package="TO92 [THT]"]

nets:
  VCC: S2.Pin_1, S2.Pin_2, S3.Pin_1, S3.Pin_2, S4.Pin_1, S4.Pin_2, S1.Pin_1, S1.Pin_2, J8.pin7, pH_Circuit1.Vcc, Часть1.5V, LCD1.VDD, T1.+Vs
  N1: S2.Pin_3, S2.Pin_4, R6.Pin_0, Часть1.A2
  N2: S3.Pin_3, S3.Pin_4, R5.Pin_0, Часть1.A1
  N3: S4.Pin_3, S4.Pin_4, R4.Pin_0, Часть1.A0
  GND: R4.Pin_1, R5.Pin_1, R6.Pin_1, J8.pin8, J8.pin9, J8.pin10, pH_Circuit1.GND#0, R7.Pin_1, Часть1.GND, LCD1.VSS, LCD1.V0, LCD1.R/W, T1.GND
  N4: S1.Pin_3, S1.Pin_4, R7.Pin_0, Часть1.A3
  N5: J8.pin1, Часть1.D13/SCK, LCD1.DB7
  N6: J8.pin2, Часть1.D11_PWM/MOSI, LCD1.DB5
  N7: J8.pin5, Часть1.D9_PWM, LCD1.E
  N8: J8.pin6, Часть1.D8, LCD1.RS
  N9: J8.pin13, Часть1.D10_PWM/SS, LCD1.DB4
  N10: J8.pin14, Часть1.D12/MISO, LCD1.DB6
  N11: U1.GND, pH_Circuit1.GND#5
  N12: U1.OUT, pH_Circuit1.PRB
  N13: pH_Circuit1.TX, Часть1.D5_PWM
  N14: pH_Circuit1.RX, Часть1.D3_PWM
  N15: Часть1.D7, T1.Vout

notes:
  pH Corrector Shield v2.5
  CyberPlant
  GND
  Vin
  http://cyberplant.info
  peristaltic pump pH Up
  peristaltic pump pH Down
