# Fritzing sketch id3154_sheeeld_0 (saved by Fritzing 0.9.3b)
breadboards: 1

parts:
  1Sheeld1 = 1Sheeld
  U1 = LCD-16X2 [package=lcd-16x2_noholes]
  R2 = Rotary Potentiometer (Small) [maximum_resistance=100kΩ package=THT]

nets:
  N1: 1Sheeld1.connector2, U1.DB7
  N2: 1Sheeld1.connector3, U1.DB6
  N3: 1Sheeld1.connector4, U1.DB5
  N4: 1Sheeld1.connector5, U1.DB4
  N5: 1Sheeld1.connector12, U1.E
  N6: 1Sheeld1.connector13, U1.RS
  N7: 1Sheeld1.connector27, U1.VSS, U1.R_W, U1.K, R2.leg2
  N8: 1Sheeld1.connector28, U1.VDD, U1.A, R2.leg1
