# Fritzing sketch id3155_sensor_schematic_0 (saved by Fritzing 0.9.2b)
circuit board: 7.37533cm x 5.47789cm
breadboards: 1

parts:
  XBee = XBEE-1 [package=xbee-1]
  TSR_1-_2434 = mystery part, 3 pins [chip_label=?]
  temp = LM35 Temperature Sensor [package="TO92 [THT]"]
  PR = PHOTOCELL [package=photocell]
  Part1 = Humidity Sensor - HIH-4030 Breakout
  Status_LED = smd LED [color="Red (633nm)" package="0805 [SMD]"]
  R2 = Resistor [tolerance=±5% resistance=220 package=THT]
  R1 = Resistor [tolerance=±5% resistance=220 package=THT]
  VCC1 = Battery block 9V

nets (from the pcb view):
  N1: XBee.VDD, TSR_1-_2434.pin3, temp.+Vs, PR.P$2
  GND: XBee.GND, TSR_1-_2434.pin2, temp.GND, Part1.GND, Status_LED.cathode, VCC1.-
  N2: XBee.DIO9, Status_LED.anode
  N3: XBee.DIO2, R1.Pin_0
  N4: XBee.DIO1, R2.Pin_0
  N5: XBee.DIO0, temp.Vout
  N6: TSR_1-_2434.pin1, Part1.VCC, VCC1.+
  N7: PR.P$1, R1.Pin_1
  N8: Part1.OUT, R2.Pin_1
