# Fritzing sketch id3156_sensor_schematic_1_0 (saved by Fritzing 0.9.2b)
circuit board: 7.5cm x 5.5cm
breadboards: 1

parts:
  XBee = XBEE-1 [package=xbee-1]
  temp = LM35 Temperature Sensor [package="TO92 [THT]"]
  PR = PHOTOCELL [package=photocell]
  Part1 = Humidity Sensor - HIH-4030 Breakout
  Status_LED = smd LED [color="Red (633nm)" package="0805 [SMD]"]
  R2 = Resistor [tolerance=±5% resistance=220 package=THT]
  R1 = Resistor [tolerance=±5% resistance=220 package=THT]
  POWER = Battery block 9V
  TSR_1-_2434 = mystery part, 3 pins [chip_label=?]
  R3 = Resistor [tolerance=±5% resistance=220 package=THT]

nets (from the pcb view):
  N1: XBee.VDD, temp.+Vs, PR.P$2, TSR_1-_2434.pin3
  GND: XBee.GND, temp.GND, Part1.GND, Part1.OUT, R2.Pin_1, R1.Pin_0, POWER.-, TSR_1-_2434.pin2, R3.Pin_0
  N2: XBee.DIO9, Status_LED.anode
  N3: XBee.DIO2, PR.P$1, R1.Pin_1
  N4: XBee.DIO1, R2.Pin_0
  N5: XBee.DIO0, temp.Vout
  N6: Part1.VCC, POWER.+, TSR_1-_2434.pin1
  N7: Status_LED.cathode, R3.Pin_1
