# Fritzing sketch id3158_Fritzing_CDbot_0 (saved by Fritzing 0.9.1b)
perfboards: 1

parts:
  L293D = H-Bridge [package=THT]
  ARDUINO_NANO = Arduino Nano (Rev3.0)
  MOTOREDUCTOR = DC Motor
  MOTOREDUCTOR_2 = DC Motor
  5V = 4 x AAA Battery Mount
  R1 = Resistor [tolerance=±5% resistance=220 package=THT]
  SENSOR_ULTRASONICO = SRF05 Ultrasonic Rangefinder
  S1 = Pushbutton [package=THT]
  S2 = Pushbutton [package=THT]
  S3 = Pushbutton [package=THT]
  R2 = Resistor [tolerance=±5% resistance=220 package=THT]
  MOTOR_DC_6V = DC Motor
  PNP_TIP30 = PNP-Transistor [package="TO92 [THT]"]
  part = Rectifier Diode [part_number=1N4001 package="300 mil [THT]"]
  R3 = Resistor [tolerance=±5% resistance=220 package=THT]
  R4 = Resistor [tolerance=±5% resistance=220 package=THT]
  part_2 = Rectifier Diode [part_number=1N4001 package="300 mil [THT]"]
  S4 = Pushbutton [package=THT]
  NPN_TIP29 = NPN-Transistor [package="TO92 [THT]"]
  NPN_TIP29_2 = NPN-Transistor [package="TO92 [THT]"]
  part_3 = Rectifier Diode [part_number=1N4001 package="300 mil [THT]"]
  part_4 = Rectifier Diode [part_number=1N4001 package="300 mil [THT]"]
  PNP_TIP30_2 = PNP-Transistor [package="TO92 [THT]"]
  VCC1 = Battery block 9V

nets (from the breadboard view):
  N1: L293D.1_2EN, ARDUINO_NANO.D5
  N2: L293D.1A, ARDUINO_NANO.D2
  N3: L293D.1Y, MOTOREDUCTOR.pin_2
  N4: L293D.2Y, MOTOREDUCTOR.pin_1
  N5: L293D.2A, ARDUINO_NANO.D4
  N6: L293D.VCC2, 5V.+, PNP_TIP30.B, PNP_TIP30.C, NPN_TIP29.B, part_3.cathode, PNP_TIP30_2.C
  N7: L293D.3_4EN, ARDUINO_NANO.D3
  N8: L293D.3A, ARDUINO_NANO.D12/MISO
  N9: L293D.3Y, MOTOREDUCTOR_2.pin_2
  GND3: L293D.GND3, L293D.GND4, ARDUINO_NANO.GND, SENSOR_ULTRASONICO.connector11, S1.leg0, S2.leg0, S3.leg0, S4.leg0, NPN_TIP29.C, VCC1.-
  N10: L293D.4Y, MOTOREDUCTOR_2.pin_1
  N11: L293D.4A, ARDUINO_NANO.D7
  N12: ARDUINO_NANO.D6, R1.Pin_1
  N13: ARDUINO_NANO.D8, SENSOR_ULTRASONICO.connector10
  N14: ARDUINO_NANO.D9, SENSOR_ULTRASONICO.connector9
  N15: ARDUINO_NANO.D11/MOSI, PNP_TIP30_2.E
  N16: ARDUINO_NANO.VIN, VCC1.+
  N17: ARDUINO_NANO.5V, SENSOR_ULTRASONICO.connector8
  N18: ARDUINO_NANO.D13/SCK, S1.leg1, S2.leg1, S3.leg1
  N19: R1.Pin_0, PNP_TIP30.E
  N20: R2.Pin_0, R3.Pin_0
  N21: R2.Pin_1, NPN_TIP29_2.E
  N22: MOTOR_DC_6V.pin_1, part_2.cathode, part_4.anode
  N23: MOTOR_DC_6V.pin_2, part.cathode, part_3.anode
  N24: R4.Pin_0, NPN_TIP29.E
  N25: part_2.anode, NPN_TIP29_2.B, part_4.cathode, PNP_TIP30_2.B
