# Fritzing sketch id315_ProtoBoard_0 (saved by Fritzing 0.8.3b)
breadboards: 1

parts:
  R1 = Resistor [tolerance=±5% resistance=220 package=THT]
  R2 = Resistor [tolerance=±5% resistance=220 package=THT]
  J1 = Basic Force Sensing Resistor (FSR) [package=THT]
  VCC1 = 4 x AAA Battery Mount
  J2 = Basic Force Sensing Resistor (FSR) [package=THT]
  R3 = Resistor [tolerance=±10% resistance=220 package=THT]
  VCC2 = 4 x AAA Battery Mount
  A1 = Amperimetro

nets:
  N1: R1.Pin_0, R2.Pin_0, A1.connector1
  N2: R1.Pin_1, R3.Pin_0, VCC2.+
  N3: R2.Pin_1, J2.pin_1, VCC2.-
  N4: J1.pin_0, VCC1.+
  N5: J1.pin_1, VCC1.-
  N6: J2.pin_0, R3.Pin_1, A1.connector0
