# Fritzing sketch id3160_proto_I_0 (saved by Fritzing 0.9.0b)
breadboards: 1

parts:
  Onderdeel1 = Arduino Uno (Rev3)
  U1 = BATTERY-2 [package=battery-aa]
  U2 = BATTERY-2 [package=battery-aa]
  U3 = BATTERY-2 [package=battery-aa]
  U4 = BATTERY-2 [package=battery-aa]
  J1 = Basic Servo
  J2 = Basic Servo
  J3 = Basic Servo
  J4 = Infrared Proximity Sensor

nets:
  N1: Onderdeel1.A0, J4.Vout
  N2: Onderdeel1.D9_PWM, J2.pulse
  N3: Onderdeel1.D10_PWM/SS, J3.pulse
  N4: Onderdeel1.D11_PWM/MOSI, J1.pulse
  N5: U1.-1, U2.+1
  GND: U1.+1, J1.gnd, J2.gnd, J3.gnd, J4.GND
  N6: U2.-1, U3.+1
  N7: U3.-1, U4.+1
  VCC: U4.-1, J1.vcc, J2.vcc, J3.vcc
