# Fritzing sketch id3164_LED_RGB_Prototype_0 (saved by Fritzing 0.9.2b)
breadboards: 1

parts:
  Part1 = Arduino Uno (Rev3)
  LED1 = RGB LED - (4 legs) [package="5 mm [THT]"]
  R1 = Resistor [tolerance=±5% resistance=220 package="1206 [SMD]"]
  R2 = Resistor [tolerance=±5% resistance=220 package="1206 [SMD]"]
  R3 = Resistor [tolerance=±5% resistance=220 package="1206 [SMD]"]

nets:
  N1: Part1.D9_PWM, R3.Pin_0
  N2: Part1.D10_PWM/SS, R2.Pin_0
  N3: Part1.D11_PWM/MOSI, R1.Pin_0
  N4: Part1.GND, LED1.common_anode
  N5: LED1.red_cathode, R1.Pin_1
  N6: LED1.green_cathode, R2.Pin_1
  N7: LED1.blue_cathode, R3.Pin_1
