# Fritzing sketch id3165_programador_attiny_84_85_0 (saved by Fritzing 0.9.3b)
circuit board: 4.20961cm x 5.2539cm
stripboards: 1

parts:
  Componente1 = Arduino Uno (Rev3)
  C1 = Electrolytic Capacitor [capacitance=1µF package="100 mil [THT, electrolytic]"]
  J1 = female pin header, 4 pins [form="♀ (female)"]
  J2 = female pin header, 1 pin [form="♀ (female)"]
  J3 = female pin header, 2 pins [form="♀ (female)"]
  J4 = female pin header, 4 pins [form="♀ (female)"]
  J6 = female pin header, 7 pins [form="♀ (female)"]
  J7 = female pin header, 7 pins [form="♀ (female)"]
  J5 = female pin header, 4 pins [form="♀ (female)"]

nets:
  N1: Componente1.D10_PWM/SS, J1.pin4, J7.pin4, J5.pin1
  N2: Componente1.D11_PWM/MOSI, J1.pin3, J4.pin4, J7.pin7
  N3: Componente1.D12/MISO, J1.pin2, J4.pin3, J6.pin7
  N4: Componente1.D13/SCK, J1.pin1, J4.pin2, J6.pin6
  N5: Componente1.RESET, C1.+, J2.pin1
  N6: Componente1.5V, J3.pin1, J4.pin1, J7.pin1
  N7: Componente1.GND, C1.-, J3.pin2, J6.pin1, J5.pin4
