# Fritzing sketch id3166_Untitled_Sketch_0 (saved by Fritzing 0.8.5b)
circuit board: 3cm x 3cm
breadboards: 1

parts:
  R1 = Resistor [tolerance=±5% resistance=220 package=THT]
  LED1 = LED - 5mm [color="Red (633nm)" package="5 mm [THT]"]
  Part1 = Arduino Uno (Rev3)
  V1 = DC Power [voltage=5]
  J1 = Screw terminal - 2 pins [package=THT]

nets:
  N1: R1.Pin_0, J1.pin1
  N2: R1.Pin_1, LED1.anode
  N3: LED1.cathode, J1.pin2
  N4: Part1.GND, V1.V-
  N5: Part1.VIN, V1.V+
