# Fritzing sketch id3167_matrix_01_0 (saved by Fritzing 0.9.3b)
breadboards: 1

parts:
  Part1 = Arduino Nano (Rev3.0)
  hc-sr1 = hc-sr04
  M1 = prefix0000

nets:
  GND: Part1.GND, hc-sr1.GND, M1.connector1
  N1: Part1.D4, hc-sr1.Echo
  N2: Part1.D5, hc-sr1.Trig
  N3: Part1.D11/MOSI, M1.connector3
  N4: Part1.D12/MISO, M1.connector4
  5V: Part1.5V, hc-sr1.VCC, M1.connector0

notes:
  M1 is a 8x8 Led Matrix. There is no part available in the library, so I used a 5 pin header.
  disregard the pin names in this view
