# Fritzing sketch id3168_Sketch_0 (saved by Fritzing 0.7.12b)
breadboards: 1

parts:
  Arduino1 = Arduino
  J1 = Basic Servo
  J3 = Infrared Proximity Sensor
  J4 = Basic Servo

nets:
  N1: Arduino1.D6, J1.pulse
  N2: Arduino1.D4, J4.pulse
  VCC: Arduino1.+5V, J1.vcc, J3.Vcc, J4.vcc
  GND: Arduino1.GND, J1.gnd, J3.GND, J4.gnd
  N3: Arduino1.A0, J3.Vout
