# Fritzing sketch id3169_schematic_0 (saved by Fritzing 0.9.1b)
breadboards: 1

parts:
  U1 = generic_sip_4_300mil.fzp [chip_label=IC]
  Part1 = Arduino Uno (Rev3)
  J1 = Piezo Speaker
  Q1 = NPN-Transistor [part_number=BC547 package="TO92 [THT]"]
  LED1 = LED - 5mm [color="Red (633nm)" package="5 mm [THT]"]
  R1 = Resistor [tolerance=±5% resistance=1k package=THT]
  R2 = Resistor [tolerance=±5% resistance=1k package=THT]

nets:
  N1: U1.connector0, Part1.5V, J1.pin2
  N2: U1.connector1, Part1.D2
  N3: U1.connector2, Part1.D3_PWM
  N4: U1.connector3, Part1.GND, Q1.C, LED1.cathode
  N5: Part1.D10_PWM/SS, R2.Pin_0
  N6: Part1.D11_PWM/MOSI, R1.Pin_1
  N7: J1.pin1, Q1.E
  N8: Q1.B, R2.Pin_1
  N9: LED1.anode, R1.Pin_0
