# Fritzing sketch id316_AMPL_2.0_0 (saved by Fritzing 0.9.3b)
breadboards: 4

parts:
  4558_2 = IC, DIP package, 8 pins [chip_label=IC]
  4558_1 = IC, DIP package, 8 pins [chip_label=IC]
  TDA7379 = STA540 [package=multiwatt15]
  C35_1000uF = CAPACITOR ELETROLITICO 1000uF
  C36_1000uF = CAPACITOR ELETROLITICO 1000uF
  ESQUERDO_SAIDA = Loudspeaker
  SUB_SAIDA = Loudspeaker
  DIREITO_SAIDA = Loudspeaker
  C37 = Electrolytic Capacitor [capacitance=100µF voltage=35V package="100 mil [THT, electrolytic]"]
  R1 = Resistor [tolerance=±5% resistance=10k package=THT]
  C38 = Electrolytic Capacitor [capacitance=10µF voltage=35V package="100 mil [THT, electrolytic]"]
  AC_TRAFO = Power Jack [package=power_jack_pth_lock]
  DC = Power Jack [package=power_jack_pth_lock]
  D1 = Rectifier Diode [part_number=1N4001 package="300 mil [THT]"]
  D2 = Rectifier Diode [part_number=1N4001 package="300 mil [THT]"]
  D3 = Rectifier Diode [part_number=1N4001 package="300 mil [THT]"]
  D4 = Rectifier Diode [part_number=1N4001 package="300 mil [THT]"]
  PONTE_RETIFICADORA_200V/4A = Resistor [tolerance=±5% resistance=220 package=THT]
  C39_6800uF = CAPACITOR ELE 6800uF-35v
  C40 = Ceramic Capacitor [capacitance=100nF voltage=35V package="100 mil [THT, multilayer]"]
  R2 = Resistor [tolerance=±5% resistance=2.7k package=THT]
  LED1 = smd LED [color="White (4500K)" package="1206 [SMD]"]
  C41 = Electrolytic Capacitor [capacitance=10µF voltage=35V package="100 mil [THT, electrolytic]"]
  R3 = Resistor [tolerance=±5% resistance=3.3k package=THT]
  R4 = Resistor [tolerance=±5% resistance=2.7k package=THT]
  C42 = Electrolytic Capacitor [capacitance=10µF voltage=35V package="100 mil [THT, electrolytic]"]
  7812_12v = Voltage Regulator - Variable [package="TO220 [THT]"]
  BASS_VOL = Rotary Potentiometer (Small) [maximum_resistance=50kΩ package=THT]
  R6 = Resistor [tolerance=±5% resistance=10k package=THT]
  C43 = Electrolytic Capacitor [capacitance=0.47µF voltage=35V package="100 mil [THT, electrolytic]"]
  C44 = Ceramic Capacitor [capacitance=100nF voltage=35V package="100 mil [THT, multilayer]"]
  C45 = Electrolytic Capacitor [capacitance=10µF voltage=35V package="100 mil [THT, electrolytic]"]
  C46 = Ceramic Capacitor [capacitance=100pF voltage=35V package="100 mil [THT, multilayer]"]
  R7 = Resistor [tolerance=±5% resistance=10k package=THT]
  C47 = Ceramic Capacitor [capacitance=220nF voltage=35V package="100 mil [THT, multilayer]"]
  R8 = Resistor [tolerance=±5% resistance=10k package=THT]
  R9 = Resistor [tolerance=±5% resistance=68k package=THT]
  R10 = Resistor [tolerance=±5% resistance=8.2k package=THT]
  R11 = Resistor [tolerance=±5% resistance=47k package=THT]
  C49 = Electrolytic Capacitor [capacitance=4.7µF package="100 mil [THT, electrolytic]"]
  R12 = Resistor [tolerance=±5% resistance=10k package=THT]
  R13 = Resistor [tolerance=±5% resistance=10k package=THT]
  C50 = Electrolytic Capacitor [capacitance=100µF voltage=35V package="100 mil [THT, electrolytic]"]
  C52 = Ceramic Capacitor [capacitance=100nF voltage=35V package="100 mil [THT, multilayer]"]
  C53 = Ceramic Capacitor [capacitance=33nF voltage=35V package="100 mil [THT, multilayer]"]
  C54 = Ceramic Capacitor [capacitance=4.7nF voltage=35V package="100 mil [THT, multilayer]"]
  R14 = Resistor [tolerance=±5% resistance=1.8k package=THT]
  R15 = Resistor [tolerance=±5% resistance=8.2k package=THT]
  C55 = Ceramic Capacitor [capacitance=6.8nF voltage=35V package="100 mil [THT, multilayer]"]
  TREBLE_R-L = POTENCIOMETRO LOG DUPLO
  R17 = Resistor [tolerance=±5% resistance=6.8k package=THT]
  C56 = Ceramic Capacitor [capacitance=33nF voltage=35V package="100 mil [THT, multilayer]"]
  R18 = Resistor [tolerance=±5% resistance=6.8k package=THT]
  C57 = Ceramic Capacitor [capacitance=4.7nF voltage=35V package="100 mil [THT, multilayer]"]
  R19 = Resistor [tolerance=±5% resistance=1.8k package=THT]
  R20 = Resistor [tolerance=±5% resistance=8.2k package=THT]
  C58 = Ceramic Capacitor [capacitance=6.8nF voltage=35V package="100 mil [THT, multilayer]"]
  C51 = Ceramic Capacitor [capacitance=100nF voltage=35V package="100 mil [THT, multilayer]"]
  R21 = Resistor [tolerance=±5% resistance=22k package=THT]
  C59 = Ceramic Capacitor [capacitance=100pF voltage=35V package="100 mil [THT, multilayer]"]
  R22 = Resistor [tolerance=±5% resistance=8.2k package=THT]
  C60 = Electrolytic Capacitor [capacitance=4.7µF voltage=35V package="100 mil [THT, electrolytic]"]
  R23 = Resistor [tolerance=±5% resistance=47k package=THT]
  C61 = Electrolytic Capacitor [capacitance=4.7µF voltage=35V package="100 mil [THT, electrolytic]"]
  C62 = Electrolytic Capacitor [capacitance=4.7µF voltage=35V package="100 mil [THT, electrolytic]"]
  R24 = Resistor [tolerance=±5% resistance=47k package=THT]
  R25 = Resistor [tolerance=±5% resistance=8.2k package=THT]
  C63 = Electrolytic Capacitor [capacitance=4.7µF voltage=35V package="100 mil [THT, electrolytic]"]
  R26 = Resistor [tolerance=±5% resistance=22k package=THT]
  C64 = Ceramic Capacitor [capacitance=100pF package="100 mil [THT, multilayer]"]
  C65 = Ceramic Capacitor [capacitance=100nF voltage=35V package="100 mil [THT, multilayer]"]
  C66 = Electrolytic Capacitor [capacitance=10µF voltage=35V package="100 mil [THT, electrolytic]"]
  R27 = Resistor [tolerance=±5% resistance=1k package=THT]
  BALANCE = Rotary Potentiometer (Small) [maximum_resistance=100k package=THT]
  R29 = Resistor [tolerance=±5% resistance=1k package=THT]
  VOLUME = POTENCIOMETRO LOG DUPLO
  ENTRADA_L-R = 2.5mm Audio Jack [package=stereojack2.5mm_stereojack2.5mm]

nets:
  N1: 4558_2.pin1, R12.Pin_0, R15.Pin_0, C55.0, R21.Pin_1, C59.1
  N2: 4558_2.pin2, R21.Pin_0, C59.0, R22.Pin_1
  N3: 4558_2.pin3, R23.Pin_0, C61.-
  N4: 4558_2.pin4, 4558_1.pin4, TDA7379.P-GND, TDA7379.S-GND, ESQUERDO_SAIDA.pin1, DIREITO_SAIDA.pin1, C38.-, DC.GND, DC.GNDBREAK, C39_6800uF.connector0, C40.0, LED1.cathode, C41.-, R4.Pin_1, C42.-, 7812_12v.ADJ, BASS_VOL.leg1, C44.0, C45.-, C46.1, C50.-, C54.1, TREBLE_R-L.connector0, TREBLE_R-L.connector3, R17.Pin_1, R18.Pin_1, C57.1, C60.-, C63.-, C65.0, C66.-, BALANCE.wiper, VOLUME.connector0, VOLUME.connector3, ENTRADA_L-R.SLEEVE
  N5: 4558_2.pin5, C62.-, R24.Pin_0
  N6: 4558_2.pin6, R25.Pin_1, R26.Pin_1, C64.1
  N7: 4558_2.pin7, R13.Pin_0, R20.Pin_0, C58.0, R26.Pin_0, C64.0
  N8: 4558_2.pin8, 4558_1.pin8, C41.+, R3.Pin_0, 7812_12v.OUT, C44.1, C45.+, C65.1, C66.+
  N9: 4558_1.pin1, R8.Pin_1, R9.Pin_1
  N10: 4558_1.pin2, R9.Pin_0, R10.Pin_1
  N11: 4558_1.pin3, R11.Pin_0
  N12: 4558_1.pin5, C46.0, R7.Pin_0
  N13: 4558_1.pin6, 4558_1.pin7, C43.+, C47.0
  N14: TDA7379.OUT1, C35_1000uF.connector1
  N15: TDA7379.OUT2, C36_1000uF.connector1
  N16: TDA7379.VCC1, TDA7379.VCC2, R1.Pin_0, C38.+, DC.PWR, D1.cathode, D3.cathode, PONTE_RETIFICADORA_200V/4A.Pin_0, C39_6800uF.connector1, C40.1, R2.Pin_0, 7812_12v.IN
  N17: TDA7379.IN1, C52.1
  N18: TDA7379.IN2, C51.1
  N19: TDA7379.SVR, C37.+
  N20: TDA7379.STBY, R1.Pin_1
  N21: TDA7379.IN4, TDA7379.IN3, R6.Pin_0
  N22: TDA7379.OUT4, SUB_SAIDA.pin2
  N23: TDA7379.OUT3, SUB_SAIDA.pin1
  N24: C35_1000uF.connector0, ESQUERDO_SAIDA.pin2
  N25: C36_1000uF.connector0, DIREITO_SAIDA.pin2
  N26: AC_TRAFO.GND, AC_TRAFO.GNDBREAK, D2.cathode, D3.anode
  N27: AC_TRAFO.PWR, D1.anode, D4.cathode
  N28: D2.anode, D4.anode, PONTE_RETIFICADORA_200V/4A.Pin_1
  N29: R2.Pin_1, LED1.anode
  N30: R3.Pin_1, R4.Pin_0, C42.+, R11.Pin_1, C49.+, R23.Pin_1, R24.Pin_1
  N31: BASS_VOL.wiper, R6.Pin_1
  N32: BASS_VOL.leg2, C43.-
  N33: R7.Pin_1, C47.1, R8.Pin_0
  N34: R10.Pin_0, C50.+
  N35: C49.-, R12.Pin_1, R13.Pin_1
  N36: C52.0, C56.1, R18.Pin_0, C57.0, R19.Pin_1
  N37: C53.0, TREBLE_R-L.connector1, TREBLE_R-L.connector2
  N38: C53.1, C54.0, R14.Pin_1, R17.Pin_0, C51.0
  N39: R14.Pin_0, R15.Pin_1, C55.1
  N40: TREBLE_R-L.connector4, TREBLE_R-L.connector5, C56.0
  N41: R19.Pin_0, R20.Pin_1, C58.1
  N42: R22.Pin_0, C60.+
  N43: C61.+, BALANCE.leg1, R29.Pin_0
  N44: C62.+, R27.Pin_0, BALANCE.leg2
  N45: R25.Pin_0, C63.+
  N46: R27.Pin_1, VOLUME.connector1
  N47: R29.Pin_1, VOLUME.connector4
  N48: VOLUME.connector2, ENTRADA_L-R.RIGHT
  N49: VOLUME.connector5, ENTRADA_L-R.LEFT

notes:
  DC ->12-18V
  AC ->9-15V
  CORRENTE ->4A
  POTENCIA 4ohm -> 2X 11W + 1X 38W
  POTENCIA 8ohm -> 2X 7W + 1X 20W
  AMPLIFICADOR
  Pontos em vermelho sao GND
