# Fritzing sketch id3170_Fritzing_Proyect_LEDs_ON_OF_en_pares_0 (saved by Fritzing 0.9.3b)
breadboards: 1

parts:
  Componente1 = Arduino Uno (Rev3)
  R1 = Resistor [tolerance=±5% resistance=220 package=THT]
  LED1 = LED - 5mm [color="Red (633nm)" package="5 mm [THT]"]
  LED2 = LED - 5mm [color="Yellow (595nm)" package="5 mm [THT]"]
  LED3 = LED - 5mm [color="Red (633nm)" package="5 mm [THT]"]
  LED4 = LED - 5mm [color="Green (570nm)" package="5 mm [THT]"]
  LED5 = LED - 5mm [color="Yellow (595nm)" package="5 mm [THT]"]
  LED6 = LED - 5mm [color="Green (570nm)" package="5 mm [THT]"]
  R2 = Resistor [tolerance=±5% resistance=220 package=THT]
  R3 = Resistor [tolerance=±5% resistance=220 package=THT]
  R4 = Resistor [tolerance=±5% resistance=220 package=THT]
  R5 = Resistor [tolerance=±5% resistance=220 package=THT]
  R6 = Resistor [tolerance=±5% resistance=220 package=THT]

nets:
  N1: Componente1.D8, LED5.anode
  N2: Componente1.D9_PWM, LED6.anode
  N3: Componente1.D4, LED1.anode
  N4: Componente1.D5_PWM, LED2.anode
  N5: Componente1.D6_PWM, LED4.anode
  N6: Componente1.D7, LED3.anode
  N7: Componente1.GND, R1.Pin_0, R2.Pin_0, R3.Pin_0, R4.Pin_0, R5.Pin_0, R6.Pin_0
  N8: R1.Pin_1, LED1.cathode
  N9: LED2.cathode, R2.Pin_1
  N10: LED3.cathode, R4.Pin_1
  N11: LED4.cathode, R3.Pin_1
  N12: LED5.cathode, R5.Pin_1
  N13: LED6.cathode, R6.Pin_1
