# Fritzing sketch id3173_Proyecto_10_Leds_0 (saved by Fritzing 0.7.10b)
breadboards: 1

parts:
  LED1 = LED - 5mm [color="Red (633nm)" package="5 mm [THT]"]
  LED2 = LED - 5mm [color="Red (633nm)" package="5 mm [THT]"]
  LED3 = LED - 5mm [color="Red (633nm)" package="5 mm [THT]"]
  LED4 = LED - 5mm [color="Red (633nm)" package="5 mm [THT]"]
  LED5 = LED - 5mm [color="Red (633nm)" package="5 mm [THT]"]
  LED6 = LED - 5mm [color="Green (565nm)" package="5 mm [THT]"]
  LED11 = LED - 5mm [color="Green (565nm)" package="5 mm [THT]"]
  LED12 = LED - 5mm [color="Green (565nm)" package="5 mm [THT]"]
  LED13 = LED - 5mm [color="Green (565nm)" package="5 mm [THT]"]
  LED14 = LED - 5mm [color="Green (565nm)" package="5 mm [THT]"]
  R1 = Resistor [tolerance=±5% resistance=120 package=THT]
  R2 = Resistor [tolerance=±5% resistance=120 package=THT]
  R3 = Resistor [tolerance=±5% resistance=120 package=THT]
  R4 = Resistor [tolerance=±5% resistance=120 package=THT]
  R5 = Resistor [tolerance=±5% resistance=120 package=THT]
  R6 = Resistor [tolerance=±5% resistance=120 package=THT]
  R7 = Resistor [tolerance=±5% resistance=120 package=THT]
  R8 = Resistor [tolerance=±5% resistance=120 package=THT]
  R10 = Resistor [tolerance=±5% resistance=120 package=THT]
  R12 = Resistor [tolerance=±5% resistance=120 package=THT]
  Arduino_Ethernet_Shield1 = Arduino Ethernet Shield

nets:
  N1: LED1.cathode, R1.Pin_0
  N2: LED1.anode, LED2.anode, LED3.anode, LED4.anode, LED5.anode, LED6.anode, LED11.anode, LED12.anode, LED13.anode, LED14.anode, Arduino_Ethernet_Shield1.+5V
  N3: LED2.cathode, R2.Pin_0
  N4: LED3.cathode, R4.Pin_0
  N5: LED4.cathode, R3.Pin_0
  N6: LED5.cathode, R8.Pin_0
  N7: LED6.cathode, R6.Pin_0
  N8: LED11.cathode, R5.Pin_0
  N9: LED12.cathode, R7.Pin_0
  N10: LED13.cathode, R12.Pin_0
  N11: LED14.cathode, R10.Pin_0
  N12: R1.Pin_1, Arduino_Ethernet_Shield1.D2
  N13: R2.Pin_1, Arduino_Ethernet_Shield1.D3
  N14: R3.Pin_1, Arduino_Ethernet_Shield1.D5
  N15: R4.Pin_1, Arduino_Ethernet_Shield1.SS#11
  N16: R5.Pin_1, Arduino_Ethernet_Shield1.D8
  N17: R6.Pin_1, Arduino_Ethernet_Shield1.D7
  N18: R7.Pin_1, Arduino_Ethernet_Shield1.D9
  N19: R8.Pin_1, Arduino_Ethernet_Shield1.D6
  N20: R10.Pin_1, Arduino_Ethernet_Shield1.MOSI
  N21: R12.Pin_1, Arduino_Ethernet_Shield1.SS#5
