# Fritzing sketch id3174_secuencia_6_ledsroxana_0 (saved by Fritzing 0.7.5b)
breadboards: 1

parts:
  R1 = Resistor [tolerance=±5% resistance=220 package=THT]
  LED1 = LED - 5mm [color="Red (633nm)" package="5 mm [THT]"]
  R2 = Resistor [tolerance=±5% resistance=220 package=THT]
  R3 = Resistor [tolerance=±5% resistance=220 package=THT]
  LED4 = LED - 5mm [color="Red (633nm)" package="5 mm [THT]"]
  R4 = Resistor [tolerance=±5% resistance=220 package=THT]
  LED5 = smd LED [color="Yellow (585nm)" package="1206 [SMD]"]
  LED11 = smd LED [color="Green (555nm)" package="1206 [SMD]"]
  R5 = Resistor [tolerance=±5% resistance=220 package=THT]
  R6 = Resistor [tolerance=±5% resistance=220 package=THT]
  LED12 = smd LED [color="Yellow (585nm)" package="1206 [SMD]"]
  LED13 = smd LED [color="Green (555nm)" package="1206 [SMD]"]
  Arduino1 = Arduino

nets:
  N1: R1.Pin_0, LED1.cathode
  N2: R1.Pin_1, R2.Pin_1, R3.Pin_1, R4.Pin_1, R5.Pin_1, R6.Pin_1
  N3: LED1.anode, Arduino1.D4
  N4: R2.Pin_0, LED5.cathode
  N5: R3.Pin_0, LED11.cathode
  N6: LED4.cathode, R4.Pin_0
  N7: LED4.anode, Arduino1.D7
  N8: LED5.anode, Arduino1.D5
  N9: LED11.anode, Arduino1.D6
  N10: R5.Pin_0, LED12.cathode
  N11: R6.Pin_0, LED13.cathode
  N12: LED12.anode, Arduino1.D8
