# Fritzing sketch id3175_escri_0 (saved by Fritzing 0.9.3b)
breadboards: 1

parts:
  LED1 = LED - 5mm [color="Red (633nm)" package="5 mm [THT]"]
  R1 = Resistor [tolerance=±5% resistance=220 package=THT]
  LED2 = LED - 5mm [color="Green (570nm)" package="5 mm [THT]"]
  R2 = Resistor [tolerance=±5% resistance=220 package=THT]
  Componente1 = Arduino Mega ADK (Rev3)

nets:
  N1: LED1.cathode, R1.Pin_1
  N2: LED1.anode, Componente1.D13_PWM
  N3: R1.Pin_0, R2.Pin_0, Componente1.GND
  N4: LED2.cathode, R2.Pin_1
  N5: LED2.anode, Componente1.D11_PWM
