# Fritzing sketch id3177_sonido_con_arduino_juli_0 (saved by Fritzing 0.7.5b)
breadboards: 1

parts:
  J2 = Piezo Speaker  # not connected
  LED1 = smd LED [color="Red (633nm)" package="1206 [SMD]"]
  R1 = Resistor [tolerance=±5% resistance=220 package=THT]
  R2 = Resistor [tolerance=±5% resistance=220 package=THT]
  LED2 = smd LED [color="Red (633nm)" package="1206 [SMD]"]
  Arduino1 = Arduino

nets:
  N1: LED1.cathode, Arduino1.D3
  N2: LED1.anode, R1.Pin_1
  N3: R1.Pin_0, R2.Pin_0, Arduino1.3V3
  N4: LED2.cathode, Arduino1.D2
