# Fritzing sketch id3178_Proyecto_de_Arduino_0 (saved by Fritzing 0.9.2b)
circuit board: 8.46667cm x 5.64444cm
breadboards: 1

parts:
  Parte1 = Arduino Uno (Rev3)
  R1 = Resistor [tolerance=±5% resistance=220 package=THT]
  R2 = Resistor [tolerance=±5% resistance=220 package=THT]
  R3 = Resistor [tolerance=±5% resistance=220 package=THT]
  S1 = Pushbutton [package="[THT]"]
  S2 = Pushbutton [package="[THT]"]
  S3 = Pushbutton [package="[THT]"]
  LED1 = LED - 5mm [color="Green (570nm)" package="5 mm [THT]"]
  LED2 = LED - 5mm [color="Orange (620nm)" package="5 mm [THT]"]
  LED3 = LED - 5mm [color="Yellow (595nm)" package="5 mm [THT]"]
  LED4 = LED - 5mm [color="Blue (505nm)" package="5 mm [THT]"]
  LED5 = LED - 5mm [color="Red (633nm)" package="5 mm [THT]"]
  R4 = Resistor [tolerance=±5% resistance=220 package=THT]
  R5 = Resistor [tolerance=±5% resistance=10 package=THT]
  R6 = Resistor [tolerance=±5% resistance=10 package=THT]
  R7 = Resistor [tolerance=±5% resistance=10 package=THT]

nets:
  N1: Parte1.D8, LED1.cathode
  N2: Parte1.D9_PWM, LED5.anode
  N3: Parte1.GND, R1.Pin_0, R2.Pin_0, R3.Pin_0, R4.Pin_1, R5.Pin_1, R6.Pin_1, R7.Pin_1
  N4: Parte1.D2, S1.Pin_1, S1.Pin_2, R7.Pin_0
  N5: Parte1.D3_PWM, S2.Pin_1, S2.Pin_2, R6.Pin_0
  N6: Parte1.D4, S3.Pin_1, S3.Pin_2, R5.Pin_0
  N7: Parte1.D5_PWM, LED3.anode
  N8: Parte1.D6_PWM, LED4.anode
  N9: Parte1.D7, LED2.anode
  N10: Parte1.5V, S1.Pin_3, S1.Pin_4
  N11: R1.Pin_1, LED2.cathode
  N12: R2.Pin_1, LED4.cathode
  N13: R3.Pin_1, LED3.cathode
  N14: S2.Pin_3, S2.Pin_4, S3.Pin_3, S3.Pin_4
  N15: LED5.cathode, R4.Pin_0
