# Fritzing sketch id318_analogInput_0 (saved by Fritzing 0.8.3b)
breadboards: 1

parts:
  part = Arduino Pro Mini v13
  R1 = Resistor [tolerance=±5% resistance=4.7 package=THT]
  R2 = Resistor [tolerance=±5% resistance=3.3k package=THT]

nets:
  N1: part.VCC, R1.Pin_1, R2.Pin_0
  N2: part.A1, R2.Pin_1
  N3: part.A0, R1.Pin_0
