# Fritzing sketch id3191_sisDigitales_0 (saved by Fritzing 0.9.3b)
breadboards: 1

parts:
  U1 = 555 Timer [package="SO8 [SMD]"]  # not connected
  VCC1 = Battery block 9V
  C1 = Electrolytic Capacitor [capacitance=1nF voltage=10V package="100 mil [THT, electrolytic]"]
  C2 = Electrolytic Capacitor [capacitance=10nF voltage=10V package="100 mil [THT, electrolytic]"]
  R1 = Resistor [tolerance=±5% resistance=10k package=THT]
  R2 = Resistor [tolerance=±5% resistance=10k package=THT]
  S2 = Pushbutton [package=THT]
  C3 = Electrolytic Capacitor [capacitance=10nF voltage=10V package="100 mil [THT, electrolytic]"]
  R3 = Resistor [tolerance=±5% resistance=220k package=THT]
  R4 = Resistor [tolerance=±5% resistance=1k package=THT]
  D1 = Rectifier Diode 10A [part_number=P1000K]  # not connected
  C4 = Electrolytic Capacitor [capacitance=2.2µF voltage=10V package="100 mil [THT, electrolytic]"]

nets:
  N1: VCC1.-, C1.+, R2.Pin_1, C3.+, C4.+
  N2: VCC1.+, C1.-, C2.-, R1.Pin_0
  N3: R1.Pin_1, R2.Pin_0, S2.leg1
  N4: S2.leg0, R3.Pin_1, C4.-
  N5: R3.Pin_0, R4.Pin_0
