# Fritzing sketch id3195_HOLAMUNDO_0 (saved by Fritzing 0.9.2b)
breadboards: 1

parts:
  Parte1 = Arduino Uno (Rev3)
  R1 = Resistor [tolerance=±5% resistance=220 package=THT]
  LED1 = LED - 5mm [color="Red (633nm)" package="5 mm [THT]"]

nets:
  N1: Parte1.D13/SCK, R1.Pin_0
  N2: Parte1.GND, LED1.cathode
  N3: R1.Pin_1, LED1.anode
