# Fritzing sketch id3196_Sal_Analog_0 (saved by Fritzing 0.9.2b)
breadboards: 1

parts:
  Parte1 = Arduino Uno (Rev3)
  LED1 = RGB LED (com. cathode, rgb) [package="5 mm [THT]"]
  R2 = Resistor [tolerance=±5% resistance=100 package=THT]
  R1 = Resistor [tolerance=±5% resistance=150 package=THT]
  R3 = Resistor [tolerance=±5% resistance=100 package=THT]

nets:
  N1: Parte1.GND, LED1.common_cathode
  N2: Parte1.D3_PWM, R3.Pin_0
  N3: Parte1.D5_PWM, R2.Pin_0
  N4: Parte1.D6_PWM, R1.Pin_0
  N5: LED1.red_anode, R1.Pin_1
  N6: LED1.green_anode, R2.Pin_1
  N7: LED1.blue_anode, R3.Pin_1
