# Fritzing sketch id3197_pt2399_0 (saved by Fritzing 0.9.2b)
circuit board: 12.1552cm x 7.84422cm
breadboards: 1

parts:
  pt2399 = IC, DIP package, 16 pins [chip_label=IC]
  0_1uf = Ceramic Capacitor [capacitance=100nF package="100 mil [THT, multilayer]"]
  100uf = Electrolytic Capacitor [capacitance=1µF package="100 mil [THT, electrolytic]"]
  + = Battery
  47uf = Ceramic Capacitor [capacitance=100nF package="100 mil [THT, multilayer]"]
  R1 = Resistor [tolerance=±5% resistance=220 package=THT]
  20k_pot = Resistor [tolerance=±5% resistance=220 package=THT]
  0_1uf_2 = Ceramic Capacitor [capacitance=100nF package="100 mil [THT, multilayer]"]
  0_1uf_3 = Ceramic Capacitor [capacitance=100nF package="100 mil [THT, multilayer]"]
  10k = Resistor [tolerance=±5% resistance=220 package=THT]
  560pf = Ceramic Capacitor [capacitance=100nF package="100 mil [THT, multilayer]"]
  10k_2 = Resistor [tolerance=±5% resistance=220 package=THT]
  15k = Resistor [tolerance=±5% resistance=220 package=THT]
  3900pf = Ceramic Capacitor [capacitance=100nF package="100 mil [THT, multilayer]"]
  4_7uf = Electrolytic Capacitor [capacitance=1µF package="100 mil [THT, electrolytic]"]
  100k = Resistor [tolerance=±5% resistance=220 package=THT]
  4_7uf_2 = Electrolytic Capacitor [capacitance=1µF package="100 mil [THT, electrolytic]"]
  5_6k = Resistor [tolerance=±5% resistance=220 package=THT]
  0_01uf = Ceramic Capacitor [capacitance=100nF package="100 mil [THT, multilayer]"]
  10uf = Electrolytic Capacitor [capacitance=1µF package="100 mil [THT, electrolytic]"]
  50k_pot = Trimmer Potentiometer [maximum_resistance=10kΩ package=THT]
  10k_3 = Resistor [tolerance=±5% resistance=220 package=THT]
  4_7k = Resistor [tolerance=±5% resistance=220 package=THT]
  10uf_2 = Electrolytic Capacitor [capacitance=1µF package="100 mil [THT, electrolytic]"]
  560pf_2 = Ceramic Capacitor [capacitance=100nF package="100 mil [THT, multilayer]"]
  15k_2 = Resistor [tolerance=±5% resistance=220 package=THT]
  3300pf = Ceramic Capacitor [capacitance=100nF package="100 mil [THT, multilayer]"]
  10k_4 = Resistor [tolerance=±5% resistance=220 package=THT]
  0_082uf = Ceramic Capacitor [capacitance=100nF package="100 mil [THT, multilayer]"]
  10k_5 = Resistor [tolerance=±5% resistance=220 package=THT]
  0_082uf_2 = Ceramic Capacitor [capacitance=100nF package="100 mil [THT, multilayer]"]

nets:
  N1: pt2399.pin1, 0_1uf.0, 100uf.+, +.-
  N2: pt2399.pin2, 47uf.1
  N3: pt2399.pin3, 0_1uf.1, 100uf.-, +.+, 47uf.0, 0_1uf_2.0, 0_1uf_3.0, 3900pf.0, 100k.Pin_0, 0_01uf.0, 50k_pot.leg2, 3300pf.1
  N4: pt2399.pin6, R1.Pin_1
  N5: pt2399.pin7, 0_1uf_2.1
  N6: pt2399.pin8, 0_1uf_3.1
  N7: pt2399.pin9, 0_082uf_2.0
  N8: pt2399.pin10, 0_082uf_2.1
  N9: pt2399.pin11, 0_082uf.0
  N10: pt2399.pin12, 0_082uf.1, 10k_5.Pin_0
  N11: pt2399.pin13, 560pf_2.0, 10k_4.Pin_0
  N12: pt2399.pin14, 5_6k.Pin_0, 560pf_2.1, 15k_2.Pin_0
  N13: pt2399.pin15, 560pf.0, 10k_2.Pin_0, 4_7k.Pin_0
  N14: pt2399.pin16, 10k.Pin_0, 560pf.1
  N15: R1.Pin_0, 20k_pot.Pin_1
  N16: 10k.Pin_1, 10k_2.Pin_1, 15k.Pin_0, 3900pf.1, 4_7uf_2.+
  N17: 15k.Pin_1, 4_7uf.+
  N18: 4_7uf.-, 100k.Pin_1
  N19: 4_7uf_2.-, 10k_3.Pin_1
  N20: 5_6k.Pin_1, 0_01uf.1, 10uf.+
  N21: 10uf.-, 50k_pot.leg1
  N22: 50k_pot.wiper, 10k_3.Pin_0
  N23: 4_7k.Pin_1, 10uf_2.+
  N24: 15k_2.Pin_1, 3300pf.0, 10k_4.Pin_1, 10k_5.Pin_1

notes:
  d-gnd
  output
  input
  pt2399 Echo application circuit
  5V
