# Fritzing sketch id3198_PuenteH_0 (saved by Fritzing 0.8.5b)
breadboards: 1

parts:
  Parte1 = Arduino Uno (Rev3)
  IC1 = L293D [package=THT]
  M1 = DC Motor
  VCC1 = Battery
  M2 = DC Motor

nets:
  N1: Parte1.D8, IC1.In_4
  N2: Parte1.D9_PWM, IC1.In_3
  N3: Parte1.D10_PWM/SS, IC1.Enable_2
  N4: Parte1.GND, IC1.0V, VCC1.-
  N5: Parte1.D2, IC1.In_1
  N6: Parte1.D3_PWM, IC1.In_2
  N7: Parte1.D5_PWM, IC1.Enable_1
  N8: IC1.Out_1_(_Controlled_by_Enable_1_), M1.pin_2
  N9: IC1.Out_2_(_Controlled_by_Enable_1_), M1.pin_1
  N10: IC1.+Vmotor, IC1.+V, VCC1.+
  N11: IC1.Out_3_(_Controlled_by_Enable_2_), M2.pin_2
  N12: IC1.Out_4_(_Controlled_by_Enable_2_), M2.pin_1
