# Fritzing sketch id3199_puenteh_0 (saved by Fritzing 0.8.4b)
breadboards: 1

parts:
  IC1 = H-Bridge [package=THT]
  Parte1 = Arduino Uno (Rev3) - ICSP
  M1 = DC Motor
  M2 = DC Motor
  VCC1 = Battery block 9V

nets:
  N1: IC1.1A, Parte1.D3_PWM
  N2: IC1.1Y, M2.pin_2
  GND1: IC1.GND1, IC1.GND2, VCC1.-
  N3: IC1.2Y, M2.pin_1
  N4: IC1.2A, Parte1.D2
  N5: IC1.VCC2, VCC1.+
  N6: IC1.3_4EN, IC1.VCC1
  N7: IC1.3A, Parte1.D4
  N8: IC1.3Y, M1.pin_2
  GND3: IC1.GND3, IC1.GND4
  N9: IC1.4Y, M1.pin_1
  N10: IC1.4A, Parte1.D5_PWM
