# Fritzing sketch id319_laserTurret_0 (saved by Fritzing 0.9.0b)
breadboards: 1

parts:
  Part2 = Arduino Uno (Rev3)
  Part4 = Thumb Joystick
  J1 = Basic Servo
  J2 = Basic Servo
  VCC1 = Battery
  LED1 = smd LED [color="Red (633nm)" package="0805 [SMD]"]

nets:
  N1: Part2.A0, Part4.HORZ
  N2: Part2.A1, Part4.VERT
  N3: Part2.D8, LED1.anode
  N4: Part2.D9_PWM, J2.pulse
  N5: Part2.D10_PWM/SS, J1.pulse
  N6: Part2.D7, Part4.SEL
  5V: Part2.5V, Part4.VCC
  GND: Part2.GND, Part4.GND, J1.gnd, J2.gnd, VCC1.-, LED1.cathode
  VCC: J1.vcc, J2.vcc, VCC1.+

notes:
  Pack of 4 AA cells
  This is a laser
  in this project
  Horizontal Servo
  Vertical Servo
  not an LED
