# Fritzing sketch id3201_proyecto2_0 (saved by Fritzing 0.9.3b)
breadboards: 1

parts:
  LED1 = LED - 5mm [color="Red (633nm)" package="5 mm [THT]"]
  S1 = Pushbutton [package="[THT]"]
  R1 = Resistor [tolerance=±5% resistance=220 package=THT]
  R2 = Resistor [tolerance=±5% resistance=220 package=THT]
  Part1 = Arduino Uno (Rev3)

nets:
  N1: LED1.cathode, R1.Pin_0
  N2: LED1.anode, Part1.D5_PWM
  N3: S1.Pin_1, S1.Pin_2, Part1.5V
  N4: S1.Pin_3, S1.Pin_4, R2.Pin_1, Part1.D6_PWM
  N5: R1.Pin_1, R2.Pin_0, Part1.GND
