# Fritzing sketch id3202_Pulsador_Timbre_0 (saved by Fritzing 0.9.2b)
circuit board: 8.46667cm x 5.64444cm
breadboards: 1

parts:
  Parte1 = Arduino Uno (Rev3)
  S1 = Pushbutton [package="[THT]"]
  R1 = Resistor [tolerance=±5% resistance=10k package=THT]
  J1 = Piezo Speaker
  LED1 = LED - 5mm [color="Red (633nm)" package="5 mm [THT]"]
  LED2 = LED - 5mm [color="Yellow (595nm)" package="5 mm [THT]"]
  R2 = Resistor [tolerance=±5% resistance=220 package=THT]
  R3 = Resistor [tolerance=±5% resistance=220 package=THT]

nets:
  N1: Parte1.D13/SCK, J1.pin2
  N2: Parte1.GND, R1.Pin_0, J1.pin1, LED1.cathode, LED2.cathode
  N3: Parte1.D2, S1.Pin_3, S1.Pin_4, R1.Pin_1
  N4: Parte1.D5_PWM, R2.Pin_0
  N5: Parte1.D7, R3.Pin_0
  N6: Parte1.5V, S1.Pin_1, S1.Pin_2
  N7: LED1.anode, R3.Pin_1
  N8: LED2.anode, R2.Pin_1
