# Fritzing sketch id3203_Pulsanti_comando_servo_0 (saved by Fritzing 0.8.0b)
breadboards: 1

parts:
  S1 = Pushbutton [package="[THT]"]
  S2 = Pushbutton [package="[THT]"]
  Arduino1 = Arduino
  J1 = Basic Servo
  R1 = Resistor [tolerance=±5% resistance=1k package=THT]
  R2 = Resistor [tolerance=±5% resistance=1k package=THT]

nets:
  N1: S1.Pin_1, S1.Pin_2, Arduino1.D3, R2.Pin_0
  +5V: S1.Pin_3, S1.Pin_4, S2.Pin_3, S2.Pin_4, Arduino1.+5V, J1.vcc
  N2: S2.Pin_1, S2.Pin_2, Arduino1.D2, R1.Pin_0
  GND: Arduino1.GND, J1.gnd, R1.Pin_1, R2.Pin_1
