# Fritzing sketch id3204_pulse_generator_0 (saved by Fritzing 0.9.2b)
breadboards: 1

parts:
  Timer_555 = 555 Timer [package="SO8 [SMD]"]
  R1 = Resistor [tolerance=±5% resistance=100k package=THT]
  POT1 = Rotary Potentiometer (Small) [maximum_resistance=1MΩ package=THT]
  C1 = Ceramic Capacitor [capacitance=10nF voltage=20V package="100 mil [THT, multilayer]"]
  VCC = Battery block 9V
  C2 = Ceramic Capacitor [capacitance=10nF voltage=20V package="100 mil [THT, multilayer]"]

nets:
  N1: Timer_555.Pin_1, C1.1, VCC.-, C2.0
  N2: Timer_555.Pin_2, Timer_555.Pin_6, R1.Pin_1, C2.1
  Output: Timer_555.Pin_3
  N3: Timer_555.Pin_4, Timer_555.Pin_8, POT1.leg1, POT1.wiper, VCC.+
  N4: Timer_555.Pin_5, C1.0
  N5: Timer_555.Pin_7, R1.Pin_0, POT1.leg2
