# Fritzing sketch id3206_alcov1_0 (saved by Fritzing 0.9.3b)
circuit board: 4.55319cm x 4.85422cm

parts:
  JP5 = Header 5x2 [package=2x5-ra]
  R9 = Resistor [tolerance=±5% resistance=220 package=THT]
  R10 = Resistor [tolerance=±5% resistance=220 package=THT]
  R11 = Resistor [tolerance=±5% resistance=220 package=THT]
  Q4 = Basic FET N-Channel [package="TO220 [THT]"]
  Q5 = Basic FET N-Channel [package="TO220 [THT]"]
  Q6 = Basic FET N-Channel [package="TO220 [THT]"]
  JP6 = Header 2 [package=screwterminal-3.5mm-2_lock]
  M4 = DC Motor
  M5 = DC Motor
  M6 = DC Motor
  R12 = Resistor [tolerance=±5% resistance=220 package=THT]
  R13 = Resistor [tolerance=±5% resistance=220 package=THT]
  R14 = Resistor [tolerance=±5% resistance=220 package=THT]

nets:
  N1: JP5.1, JP5.2, R11.Pin_1
  N2: JP5.3, JP5.4, R10.Pin_1
  N3: JP5.5, JP5.6, R9.Pin_1
  N4: R9.Pin_0, Q5.gate, R13.Pin_0
  N5: R10.Pin_0, Q6.gate, R12.Pin_0
  N6: R11.Pin_0, Q4.gate, R14.Pin_0
  N7: Q4.drain, M4.pin_2, R14.Pin_1
  N8: Q4.source, Q5.source, Q6.source, JP6.2
  N9: Q5.drain, M6.pin_2, R13.Pin_1
  N10: Q6.drain, M5.pin_2, R12.Pin_1
  N11: JP6.1, M4.pin_1, M5.pin_1, M6.pin_1
