# Fritzing sketch id3207_Shift_Register_push_button_circuit_0 (saved by Fritzing 0.9.0b)
breadboards: 1

parts:
  R2 = Resistor [tolerance=±5% resistance=220 package=THT]
  R3 = Resistor [tolerance=±5% resistance=220 package=THT]
  R4 = Resistor [tolerance=±5% resistance=220 package=THT]
  R5 = Resistor [tolerance=±5% resistance=220 package=THT]
  R6 = Resistor [tolerance=±5% resistance=220 package=THT]
  R7 = Resistor [tolerance=±5% resistance=220 package=THT]
  R8 = Resistor [tolerance=±5% resistance=220 package=THT]
  R1 = Resistor [tolerance=±5% package="0402 [SMD]"]
  LED2 = LED - 5mm [color="Red (633nm)" package="5 mm [THT]"]
  LED3 = LED - 5mm [color="Red (633nm)" package="5 mm [THT]"]
  LED4 = LED - 5mm [color="Red (633nm)" package="5 mm [THT]"]
  LED5 = LED - 5mm [color="Red (633nm)" package="5 mm [THT]"]
  LED6 = LED - 5mm [color="Red (633nm)" package="5 mm [THT]"]
  LED7 = LED - 5mm [color="Red (633nm)" package="5 mm [THT]"]
  LED8 = LED - 5mm [color="Red (633nm)" package="5 mm [THT]"]
  LED9 = LED - 5mm [color="Red (633nm)" package="5 mm [THT]"]
  U1 = 74HC595 [package="DIP16 [THT]"]
  S4 = Pushbutton [package="[THT]"]
  S5 = Pushbutton [package="[THT]"]
  S6 = Pushbutton [package="[THT]"]
  R9 = Resistor [tolerance=±5% resistance=220 package="0603 [SMD]"]
  R10 = Resistor [tolerance=±5% resistance=220 package="0603 [SMD]"]
  R11 = Resistor [tolerance=±5% resistance=220 package="0603 [SMD]"]
  LED10 = smd LED [color="Red (633nm)" package="0805 [SMD]"]
  LED11 = smd LED [color="Red (633nm)" package="0805 [SMD]"]
  LED12 = smd LED [color="Red (633nm)" package="0805 [SMD]"]

nets:
  N1: R2.Pin_0, U1.Q7
  N2: R2.Pin_1, LED9.anode
  N3: R3.Pin_0, U1.Q0
  N4: R3.Pin_1, LED2.anode
  N5: R4.Pin_0, U1.Q1
  N6: R4.Pin_1, LED3.anode
  N7: R5.Pin_0, U1.Q2
  N8: R5.Pin_1, LED4.anode
  N9: R6.Pin_0, U1.Q3
  N10: R6.Pin_1, LED5.anode
  N11: R7.Pin_0, U1.Q4
  N12: R7.Pin_1, LED6.anode
  N13: R8.Pin_0, U1.Q5
  N14: R8.Pin_1, LED7.anode
  N15: R1.Pin_0, U1.Q6
  N16: R1.Pin_1, LED8.anode
  N17: LED2.cathode, LED3.cathode, LED4.cathode, LED5.cathode, LED6.cathode, LED7.cathode, LED8.cathode, LED9.cathode, U1.GND, U1.OE, S4.Pin_3, S4.Pin_4, LED10.anode, LED11.anode, LED12.anode
  N18: U1.MR, U1.VCC, S5.Pin_3, S5.Pin_4, S6.Pin_3, S6.Pin_4
  N19: U1.SH_CP, S5.Pin_1, S5.Pin_2, R10.Pin_0
  N20: U1.ST_CP, S6.Pin_1, S6.Pin_2, R11.Pin_0
  N21: U1.DS, S4.Pin_1, S4.Pin_2, R9.Pin_0
  N22: R9.Pin_1, LED11.cathode
  N23: R10.Pin_1, LED10.cathode
  N24: R11.Pin_1, LED12.cathode
