# Fritzing sketch id3210_Matrix_Switch_0 (saved by Fritzing 0.8.7b)
circuit board: 8.93198cm x 6.1522cm
breadboards: 2

parts:
  Disp2 = generic_female_pin_header_2_100mil.fzp [part_number=LBT2088AH]
  R5 = Resistor [tolerance=±5% resistance=220 package=THT]
  R6 = Resistor [tolerance=±5% resistance=220 package=THT]
  R7 = Resistor [tolerance=±5% resistance=220 package=THT]
  R8 = Resistor [tolerance=±5% resistance=220 package=THT]
  R9 = Resistor [tolerance=±5% resistance=220 package=THT]
  R10 = Resistor [tolerance=±5% resistance=220 package=THT]
  R11 = Resistor [tolerance=±5% resistance=220 package=THT]
  R12 = Resistor [tolerance=±5% resistance=220 package=THT]
  part = Resistor [tolerance=±5% resistance=220 package=THT]  # not connected
  Arduino1 = Arduino Uno (Rev3)
  S1 = Pushbutton [package=THT]
  R13 = Resistor [tolerance=±5% resistance=100k package=THT]
  R13_2 = Resistor [tolerance=±5% resistance=100k package=THT]

nets:
  N1: Disp2.connector0, R9.Pin_1
  N2: Disp2.connector1, R11.Pin_1
  N3: Disp2.connector2, Arduino1.D3_PWM
  N4: Disp2.connector3, Arduino1.D2
  N5: Disp2.connector4, R12.Pin_1
  N6: Disp2.connector6, Arduino1.A1
  N7: Disp2.connector7, R10.Pin_1
  N8: Disp2.connector8, R7.Pin_1
  N9: Disp2.connector9, R5.Pin_1
  N10: Disp2.connector10, Arduino1.D12/MISO
  N11: Disp2.connector11, Arduino1.D11_PWM/MOSI
  N12: Disp2.connector12, R6.Pin_1
  N13: Disp2.connector13, Arduino1.D9_PWM
  N14: Disp2.connector14, R8.Pin_1
  N15: Disp2.connector15, Arduino1.D7
  N16: Disp2.connector16, Arduino1.D6_PWM
  N17: R5.Pin_0, Arduino1.A4/SDA, Arduino1.D13/SCK, S1.leg1, R13.Pin_1, R13_2.Pin_1
  N18: R6.Pin_0, Arduino1.D10_PWM/SS
  N19: R7.Pin_0, Arduino1.A3
  N20: R8.Pin_0, Arduino1.D8
  N21: R9.Pin_0, Arduino1.D5_PWM
  N22: R10.Pin_0, Arduino1.A2
  N23: R11.Pin_0, Arduino1.D4
  N24: R12.Pin_0, Arduino1.A0
  N25: Arduino1.5V, R13.Pin_0, R13_2.Pin_0

notes:
  MATRIX
