# Fritzing sketch id3211_BushButtun_Notification_0 (saved by Fritzing 0.9.2b)
breadboards: 1

parts:
  パーツ1 = Arduino Yun
  S1 = Pushbutton [package="[THT]"]
  R1 = Resistor [tolerance=±5% resistance=10k package=THT]

nets:
  N1: パーツ1.GND, R1.Pin_1
  N2: パーツ1.D4, パーツ1.3V3, S1.Pin_1, S1.Pin_2, S1.Pin_3, S1.Pin_4, R1.Pin_0
