# Fritzing sketch id321_Analog_Magnet_finder_0 (saved by Fritzing 0.3.12b)
breadboards: 1

parts:
  S2 = Reed switch [package=THT]
  S3 = Reed switch [package=THT]
  VCC1 = obsolete Battery
  DI1 = 7-Segment LED Display [package=THT]
  LED1 = Red LED - 5mm
  S4 = Toggle Switch [package=THT]
  J1 = Piezo Speaker
  S5 = Reed switch [package=THT]

nets:
  N1: S2.pin_1, S3.pin_1, VCC1.-, VCC1.+, LED1.cathode, LED1.anode, S4.COM, S5.pin_1
  N2: S2.pin_2, S3.pin_2, DI1.cathodeE, DI1.cathodeD, DI1.cathodeC, DI1.cathodeB, DI1.cathodeA, DI1.cathodeF, J1.pin1, S5.pin_2
  N3: DI1.commAnode#7, S4.L1, J1.pin2

notes:
  Analog Magnet Finder Made by Brett Monty
