# Fritzing sketch id3225_16_PWM___DAC_Fan_Control_Fritzing_0 (saved by Fritzing 0.8.7b)
breadboards: 1

parts:
  Part1 = Arduino Uno (Rev3)
  T1 = LM35 Temperature Sensor [package="TO92 [THT]"]
  Q1 = NPN-Transistor [package="TO92 [THT]"]
  M1 = DC Motor
  R1 = Resistor [tolerance=±5% resistance=220 package=THT]

nets:
  N1: Part1.A0, T1.Vout
  N2: Part1.D13/SCK, R1.Pin_0
  GND: Part1.GND, T1.GND
  N3: Part1.5V, T1.+Vs
  N4: Q1.E, M1.pin_1
  N5: Q1.B, R1.Pin_1
  N6: Q1.C, M1.pin_2
