# Fritzing sketch id3226_15_PWM___DAC_LED_Control_Fritzing_0 (saved by Fritzing 0.8.7b)
breadboards: 1

parts:
  Part1 = Arduino Uno (Rev3)
  LED1 = LED - 5mm [color="Red (633nm)" package="5 mm [THT]"]
  R1 = Resistor [tolerance=±5% resistance=220 package=THT]
  R2 = Rotary Potentiometer (Small) [maximum_resistance=100kΩ package=THT]

nets:
  N1: Part1.A0, R2.wiper
  N2: Part1.D13/SCK, R1.Pin_0
  N3: Part1.GND, LED1.cathode, R2.leg2
  N4: Part1.5V, R2.leg1
  N5: LED1.anode, R1.Pin_1
