# Fritzing sketch id3227_PWM_Demo_0 (saved by Fritzing 0.9.3b)
breadboards: 1

parts:
  WeMos_D1_Mini1 = WeMos D1 Mini
  R1 = Rotary Potentiometer (Large) [maximum_resistance=10kΩ package=THT]
  R2 = Resistor [tolerance=±5% resistance=100 package="1206 [SMD]"]
  LED2 = LEDs [package=led10mm]

nets:
  N1: WeMos_D1_Mini1.3V3, R1.leg1
  N2: WeMos_D1_Mini1.A0, R1.wiper
  N3: WeMos_D1_Mini1.D0, LED2.A
  N4: WeMos_D1_Mini1.G, R1.leg2, R2.Pin_0
  N5: R2.Pin_1, LED2.C
