# Fritzing sketch id3228_PWM_Expander_0 (saved by Fritzing 0.3.12b)
breadboards: 1

parts:
  Arduino = Arduino
  ERR = Red LED - 5mm
  TLC5940NT = IC, DIP package, 28 pins [chip_label=TLC5940NT spacing=300mil]
  PWR = green LED - 5mm
  R1 = Resistor [resistance=220 package=THT]
  R1_2 = Resistor [resistance=220 package=THT]
  R2 = Resistor [resistance=2.2k package=THT]
  J3 = screw terminal, 8 pins
  J3_2 = screw terminal, 8 pins
  R3 = Resistor [resistance=10k package=THT]
  J3_3 = screw terminal, 8 pins

nets:
  N1: Arduino.GND, TLC5940NT.pin22, TLC5940NT.pin27, PWR.cathode, R2.Pin_0, R3.Pin_0
  N2: Arduino.D13, TLC5940NT.pin25
  N3: Arduino.D11, TLC5940NT.pin26
  N4: Arduino.D10, TLC5940NT.pin23, R3.Pin_1
  N5: Arduino.D9, TLC5940NT.pin24
  N6: Arduino.D3, TLC5940NT.pin18
  N7: Arduino.+5V, TLC5940NT.pin19, TLC5940NT.pin21, R1.Pin_1, R1_2.Pin_1, J3_3.pin1, J3_3.pin2, J3_3.pin3, J3_3.pin4, J3_3.pin5, J3_3.pin6, J3_3.pin7, J3_3.pin8
  N8: ERR.cathode, TLC5940NT.pin16
  N9: ERR.anode, R1_2.Pin_0
  N10: TLC5940NT.pin1, J3.pin2
  N11: TLC5940NT.pin2, J3.pin3
  N12: TLC5940NT.pin3, J3.pin4
  N13: TLC5940NT.pin4, J3.pin5
  N14: TLC5940NT.pin5, J3.pin6
  N15: TLC5940NT.pin6, J3.pin7
  N16: TLC5940NT.pin7, J3.pin8
  N17: TLC5940NT.pin8, J3_2.pin1
  N18: TLC5940NT.pin9, J3_2.pin2
  N19: TLC5940NT.pin10, J3_2.pin3
  N20: TLC5940NT.pin11, J3_2.pin4
  N21: TLC5940NT.pin12, J3_2.pin5
  N22: TLC5940NT.pin13, J3_2.pin6
  N23: TLC5940NT.pin14, J3_2.pin7
  N24: TLC5940NT.pin15, J3_2.pin8
  N25: TLC5940NT.pin20, R2.Pin_1
  N26: TLC5940NT.pin28, J3.pin1
  N27: PWR.anode, R1.Pin_0
