# Fritzing sketch id3229_rgbpwmkontrol_0 (saved by Fritzing 0.8.7b)
breadboards: 1

parts:
  Eleman1 = Arduino Uno (Rev3)
  LED1 = RGB LED (com. anode, rbg) [package="5 mm [THT]"]
  R1 = Resistor [tolerance=±5% resistance=220 package=THT]
  R2 = Resistor [tolerance=±5% resistance=220 package=THT]
  R3 = Resistor [tolerance=±5% resistance=220 package=THT]
  S1 = Pushbutton [package="[THT]"]
  R4 = Resistor [tolerance=±5% resistance=10k package=THT]

nets:
  N1: Eleman1.D9_PWM, R3.Pin_0
  N2: Eleman1.D10_PWM/SS, R2.Pin_0
  N3: Eleman1.D11_PWM/MOSI, R1.Pin_0
  N4: Eleman1.D4, S1.Pin_1, S1.Pin_2, R4.Pin_0
  N5: Eleman1.5V, S1.Pin_3, S1.Pin_4
  N6: Eleman1.GND, LED1.common_anode, R4.Pin_1
  N7: LED1.red_cathode, R1.Pin_1
  N8: LED1.blue_cathode, R2.Pin_1
  N9: LED1.green_cathode, R3.Pin_1
