# Fritzing sketch id322_Z_Wave_Z_Uno_lm335_0 (saved by Fritzing 0.9.2b)
breadboards: 1

parts:
  Z-uno_2_1 = zuno2
  T1 = LM35 Temperature Sensor [package="TO92 [THT]"]
  R2 = Resistor [tolerance=±5% resistance=300 package=THT]

nets:
  N1: Z-uno_2_1.connector3, T1.GND
  N2: Z-uno_2_1.connector4, R2.Pin_1
  N3: Z-uno_2_1.connector10, T1.Vout, R2.Pin_0
  N4: Z-uno_2_1.connector17, Z-uno_2_1.connector18
  N5: Z-uno_2_1.connector41, Z-uno_2_1.connector44
  N6: Z-uno_2_1.connector42, Z-uno_2_1.connector43
