# Fritzing sketch id3230_17_PWM___LDR_Brigntness_Control_Fritzing_0 (saved by Fritzing 0.8.7b)
breadboards: 1

parts:
  Part1 = Arduino Uno (Rev3)
  R1 = Resistor [tolerance=±5% resistance=220 package=THT]
  R3 = Photocell (LDR) [package=THT]
  LED1 = LED - 5mm [color="Red (633nm)" package="5 mm [THT]"]
  R2 = Resistor [tolerance=±5% resistance=220 package=THT]

nets:
  N1: Part1.A0, R1.Pin_1, R3.pin_0
  N2: Part1.D13/SCK, R2.Pin_0
  N3: Part1.GND, R3.pin_1, LED1.cathode
  N4: Part1.5V, R1.Pin_0
  N5: LED1.anode, R2.Pin_1
