# Fritzing sketch id3231_PWM+motorDC_0 (saved by Fritzing 0.8.5b)
breadboards: 1

parts:
  IC1 = IC, DIP package, 8 pins [chip_label="555 "]
  D1 = Rectifier Diode [part_number=1N4001 package="300 mil [THT]"]
  D2 = Rectifier Diode [part_number=1N4001 package="300 mil [THT]"]
  R1 = Rotary Potentiometer (Small) [maximum_resistance=100kΩ package=THT]
  C1 = Ceramic Capacitor [capacitance=100nF package="100 mil [THT, multilayer]"]
  R2 = Resistor [tolerance=±5% resistance=10k package=THT]
  LED1 = LED - 5mm [color="Red (633nm)" package="5 mm [THT]"]
  R3 = Resistor [tolerance=±5% resistance=4.7k package=THT]
  Q1 = NPN-Transistor [package="TO92 [THT]"]
  R4 = Resistor [tolerance=±5% resistance=1k package=THT]
  D3 = Rectifier Diode [part_number=1N4001 package="300 mil [THT]"]
  M1 = DC Motor

nets:
  N1: IC1.pin1, C1.0, Q1.E
  N2: IC1.pin2, IC1.pin6, D1.cathode, D2.anode, C1.1
  N3: IC1.pin3, R1.wiper
  N4: IC1.pin7, R2.Pin_1, LED1.anode
  N5: IC1.pin8, R2.Pin_0
  N6: D1.anode, R1.leg1
  N7: D2.cathode, R1.leg2
  N8: LED1.cathode, R3.Pin_1
  N9: Q1.B, R4.Pin_1
  N10: Q1.C, D3.anode, M1.pin_2
  N11: D3.cathode, M1.pin_1
