# Fritzing sketch id3232_18_PWM___Programmable_Voltage_Source_Fritzing_0 (saved by Fritzing 0.8.7b)
breadboards: 1

parts:
  Part1 = Arduino Uno (Rev3)
  R1 = Resistor [tolerance=±10% resistance=1k package=THT]
  C1 = Tantalum Capacitor [capacitance=0.1mF package="100 mil [THT, tantalum]"]
  J1 = Screw terminal - 2 pins [package=THT]

nets:
  N1: Part1.D9_PWM, R1.Pin_0
  N2: Part1.GND, C1.-, J1.pin2
  N3: R1.Pin_1, C1.+, J1.pin1

notes:
  [volt meter]
