# Fritzing sketch id3233_Speed_Controller_0 (saved by Fritzing 0.9.0b)
circuit board: 3.17484cm x 4.96366cm
breadboards: 1

parts:
  D2 = Rectifier Diode [part_number=1N4001 package="300 mil [THT]"]
  U1 = 555 Timer [part_number=276-1723 package="DIP8 [THT]"]
  R2 = Resistor [tolerance=±5% resistance=10k part_number=271-006 package=THT]
  C1 = Electrolytic Capacitor [capacitance=0.1mF voltage=35V part_number=272-1016 package="100 mil [THT, electrolytic]"]
  Q1 = Basic FET N-Channel [part_number="276-2072 (IRF510 Transistor)" package="TO220 [THT]"]
  D3 = Rectifier Diode [part_number=1N4001 package="300 mil [THT]"]
  R1 = Rotary Potentiometer (Large) [maximum_resistance=100kΩ part_number=271-1722 package=THT]
  J1 = screw terminal, 2 pins [part_number=276-1388]
  J2 = screw terminal, 2 pins [part_number=276-1388]
  J4 = screw terminal, 2 pins [part_number=276-1388]
  D1 = Rectifier Diode [part_number=1N4001 package="300 mil [THT]"]
  J3 = screw terminal, 2 pins [part_number=276-1388]
  C3 = Ceramic Capacitor [capacitance=100nF voltage=50V part_number=272-135 package="100 mil [THT, multilayer]"]
  C4 = Ceramic Capacitor [capacitance="100 nF" voltage=50V part_number=272-135 package="100 mil [THT, multilayer]"]

nets:
  N1: D2.cathode, R1.leg2, J4.pin2
  N2: D2.anode, U1.Trigger, U1.Threshold, D1.cathode, C3.1
  N3: U1.Ground, C1.-, Q1.source, J1.pin2, C3.0, C4.1
  N4: U1.Output, R1.wiper, J4.pin1
  N5: U1.Reset, U1.Vcc_Supply_Voltage, R2.Pin_1, C1.+, D3.cathode, J1.pin1, J2.pin1
  N6: U1.Control_Voltage, C4.0
  N7: U1.Discharge, R2.Pin_0, Q1.gate
  N8: Q1.drain, D3.anode, J2.pin2
  N9: R1.leg1, D1.anode, J3.pin2

notes:
  Power in
  Frequency Modulated Power out
