# Fritzing sketch id3234_Arduino_TLC5940_PWM_0 (saved by Fritzing 0.8.5b)
breadboards: 2

parts:
  Part1 = Arduino Uno (Rev3)
  U1 = 74HC04_HEX_INVERTER [package=dil14]
  U2 = 74HC04_HEX_INVERTER [package=dil14]
  TLC5940 = Packages: [package=dil28-3]
  R1 = Resistor [tolerance=±1% resistance=2k package=THT]
  U3 = 74HC04_HEX_INVERTER [package=dil14]
  R3 = Resistor [tolerance=±5% resistance=1k package=THT]
  R4 = Resistor [tolerance=±5% resistance=1k package=THT]
  R5 = Resistor [tolerance=±5% resistance=1k package=THT]
  R6 = Resistor [tolerance=±5% resistance=1k package=THT]
  R7 = Resistor [tolerance=±5% resistance=1k package=THT]
  R8 = Resistor [tolerance=±5% resistance=1k package=THT]
  R9 = Resistor [tolerance=±5% resistance=1k package=THT]
  R10 = Resistor [tolerance=±5% resistance=1k package=THT]
  R11 = Resistor [tolerance=±5% resistance=1k package=THT]
  R12 = Resistor [tolerance=±5% resistance=1k package=THT]
  R13 = Resistor [tolerance=±5% resistance=1k package=THT]
  R14 = Resistor [tolerance=±5% resistance=1k package=THT]
  R15 = Resistor [tolerance=±5% resistance=1k package=THT]
  R16 = Resistor [tolerance=±5% resistance=1k package=THT]
  R17 = Resistor [tolerance=±5% resistance=1k package=THT]
  R18 = Resistor [tolerance=±5% resistance=1k package=THT]

nets:
  N1: Part1.D9_PWM, TLC5940.OUT10
  N2: Part1.D10_PWM/SS, TLC5940.OUT9
  N3: Part1.D11_PWM/MOSI, TLC5940.OUT12
  N4: Part1.D13/SCK, TLC5940.OUT11
  N5: Part1.D3_PWM, TLC5940.OUT4
  VCC: Part1.5V, U1.VCC, U2.VCC, TLC5940.OUT5, TLC5940.OUT7, U3.VCC, R3.Pin_1, R4.Pin_1, R5.Pin_1, R6.Pin_0, R7.Pin_0, R8.Pin_0, R9.Pin_0, R10.Pin_0, R11.Pin_0, R12.Pin_0, R13.Pin_0, R14.Pin_0, R15.Pin_1, R16.Pin_1, R17.Pin_1, R18.Pin_1
  GND: Part1.GND, U1.GND, U2.GND, TLC5940.OUT8, TLC5940.OUT13, R1.Pin_1, U3.GND
  N6: U1.1A, TLC5940.OUT1, R5.Pin_0
  N7: U1.2A, TLC5940.SCLK, R4.Pin_0
  N8: U1.3A, TLC5940.XLAT, R3.Pin_0
  N9: U1.4A, TLC5940.SIN, R8.Pin_1
  N10: U1.5A, TLC5940.VPRG, R7.Pin_1
  N11: U1.6A, TLC5940.OUT0, R6.Pin_1
  N12: U2.1A, TLC5940.OUT14, R18.Pin_0
  N13: U2.2A, TLC5940.DCPRG, R17.Pin_0
  N14: U2.3A, TLC5940.GSCLK, R16.Pin_0
  N15: U2.4A, TLC5940.SOUT, R11.Pin_1
  N16: U2.5A, TLC5940.XERR, R10.Pin_1
  N17: U2.6A, TLC5940.OUT15, R9.Pin_1
  N18: TLC5940.OUT6, R1.Pin_0
  N19: TLC5940.IREF, U3.6A, R12.Pin_1
  N20: TLC5940.VCC, U3.5A, R13.Pin_1
  N21: TLC5940.GND, U3.4A, R14.Pin_1
  N22: TLC5940.BLANK, U3.3A, R15.Pin_0

notes:
  PWM Out Ch. 15~0
