# Fritzing sketch id3235_pydrum_0 (saved by Fritzing 0.9.3b)
breadboards: 1

parts:
  IC1 = IC, DIP package, 16 pins [chip_label=MCP3008]
  R2 = Resistor [tolerance=±5% resistance=1M power=2W package=THT]
  R3 = Resistor [tolerance=±5% resistance=1M package=THT]
  R4 = Resistor [tolerance=±5% resistance=1M package=THT]
  R5 = Resistor [tolerance=±5% resistance=1M package=THT]
  R6 = Resistor [tolerance=±5% resistance=1M package=THT]
  R8 = Resistor [tolerance=±5% resistance=1M package=THT]
  R9 = Resistor [tolerance=±5% resistance=1M package=THT]
  bass_drum = Piezo Speaker
  crash = Piezo Speaker
  tom = Piezo Speaker
  ride = Piezo Speaker
  floor_tom = Piezo Speaker
  snare = Piezo Speaker
  hihat = Piezo Speaker
  Raspberry_Pi1 = Raspberry Pi 2
  Hihat_padel = HALL-EFFECT [package=sc70]

nets:
  N1: IC1.pin1, Hihat_padel.OUT
  N2: IC1.pin2, R2.Pin_0, crash.pin2
  N3: IC1.pin3, R3.Pin_0, hihat.pin2
  N4: IC1.pin4, R9.Pin_0, snare.pin2
  N5: IC1.pin5, R5.Pin_0, tom.pin2
  N6: IC1.pin6, R6.Pin_0, floor_tom.pin2
  N7: IC1.pin7, R8.Pin_0
  N8: IC1.pin8, R4.Pin_0, bass_drum.pin2
  GND: IC1.pin9, IC1.pin14, R2.Pin_1, R3.Pin_1, R4.Pin_1, R5.Pin_1, R6.Pin_1, R8.Pin_1, R9.Pin_1, bass_drum.pin1, crash.pin1, tom.pin1, ride.pin1, floor_tom.pin1, snare.pin1, hihat.pin1, Raspberry_Pi1.GND, Hihat_padel.GND
  N9: IC1.pin10, Raspberry_Pi1.GPIO8
  N10: IC1.pin11, Raspberry_Pi1.GPIO10
  N11: IC1.pin12, Raspberry_Pi1.GPIO9
  N12: IC1.pin13, Raspberry_Pi1.GPIO11
  N13: IC1.pin15, IC1.pin16, Hihat_padel.VCC

notes:
  Pydrum - https://github.com/PCMan/pydrum
  Copyright (C) 2016 Hong Jen Yee (PCMan) <pcman.tw@gmail.com>
