# Fritzing sketch id3236_Dani_Ampel_0 (saved by Fritzing 0.9.2b)
circuit board: 8.46667cm x 5.64444cm
breadboards: 1

parts:
  Bauteil1 = Arduino Uno (Rev3)
  R2 = Resistor [tolerance=±5% resistance=220 package="2010 [SMD]"]  # not connected
  R3 = Resistor [tolerance=±5% resistance=220 package="2010 [SMD]"]  # not connected
  R4 = Resistor [tolerance=±5% resistance=220 package="2010 [SMD]"]  # not connected
  R5 = Resistor [tolerance=±5% resistance=220 package="2010 [SMD]"]  # not connected
  R6 = Resistor [tolerance=±5% resistance=220 package="2010 [SMD]"]  # not connected
  R7 = Resistor [tolerance=±5% resistance=220 package="2010 [SMD]"]  # not connected
  R8 = Resistor [tolerance=±5% resistance=220 package="2010 [SMD]"]  # not connected
  R9 = Resistor [tolerance=±5% resistance=220 package="2010 [SMD]"]  # not connected
  R10 = Resistor [tolerance=±5% resistance=220 package="2010 [SMD]"]  # not connected
  S3 = Pushbutton [package="[THT]"]
  S4 = Pushbutton [package="[THT]"]
  R11 = Resistor [tolerance=±5% resistance=220 package=THT]
  R12 = Resistor [tolerance=±5% resistance=220 package=THT]
  LED1 = smd LED [color="Red (633nm)" package="1206 [SMD]"]  # not connected
  LED3 = smd LED [color="Red (633nm)" package="1206 [SMD]"]
  LED4 = smd LED [color="Red (633nm)" package="1206 [SMD]"]
  S5 = Pushbutton [package="[THT]"]
  R13 = Resistor [tolerance=±5% resistance=220 package=THT]
  LED8 = LED - 5mm [color="Red (633nm)" package="5 mm [THT]"]
  J1 = Piezo Speaker  # not connected
  LED12 = LED - 5mm [color="Yellow (592nm)" package="5 mm [THT]"]
  LED13 = LED - 5mm [color="Yellow (592nm)" package="5 mm [THT]"]
  LED14 = LED - 5mm [color="Green (555nm)" package="5 mm [THT]"]
  LED15 = LED - 5mm [color="Green (555nm)" package="5 mm [THT]"]
  LED16 = LED - 5mm [color="Green (555nm)" package="5 mm [THT]"]
  LED17 = LED - 5mm [color="Green (555nm)" package="5 mm [THT]"]

nets:
  N1: Bauteil1.D9_PWM, LED16.anode, LED17.anode
  N2: Bauteil1.D10_PWM/SS, LED3.anode, LED4.anode
  N3: Bauteil1.D11_PWM/MOSI, LED14.anode, LED15.anode
  N4: Bauteil1.D12/MISO, LED12.anode, LED13.anode
  N5: Bauteil1.D13/SCK, LED8.anode
  N6: Bauteil1.GND, R11.Pin_1, R12.Pin_1, R13.Pin_1
  N7: Bauteil1.D1/TX, S5.Pin_1, S5.Pin_2, R13.Pin_0
  N8: Bauteil1.D3_PWM, S4.Pin_1, S4.Pin_2, R12.Pin_0
  N9: Bauteil1.5V, S3.Pin_3, S3.Pin_4, S4.Pin_3, S4.Pin_4, S5.Pin_3, S5.Pin_4
  N10: S3.Pin_1, S3.Pin_2, R11.Pin_0
