# Fritzing sketch id3237_Siewsrichol_Arduino_Sketch_0 (saved by Fritzing 0.9.0b)
breadboards: 1

parts:
  Part1 = Arduino Uno (Rev3)
  U1 = TEMPERATURE-SENSOR [package=to-92]
  J1 = Piezo Speaker
  LED1 = LED - 5mm [color="Red (633nm)" package="5 mm [THT]"]
  LED2 = LED - 5mm [color="Red (633nm)" package="5 mm [THT]"]
  LED3 = LED - 5mm [color="Red (633nm)" package="5 mm [THT]"]
  LED4 = LED - 5mm [color="Red (633nm)" package="5 mm [THT]"]
  LED5 = Super Flux LED blue [color=Blue]
  R1 = Resistor [package="2512 [SMD]"]
  R2 = Resistor [package="2512 [SMD]"]
  R3 = Resistor [package="2512 [SMD]"]
  R4 = Resistor [package="2512 [SMD]"]
  R5 = Resistor [package="2512 [SMD]"]
  S1 = Pushbutton [package="[THT]"]
  S2 = Pushbutton [package="[THT]"]
  R6 = Resistor [package="0402 [SMD]"]
  R7 = Resistor [package="0402 [SMD]"]

nets:
  N1: Part1.A0, U1.ADJ
  N2: Part1.A1, S1.Pin_3, S1.Pin_4
  N3: Part1.A2, S2.Pin_3, S2.Pin_4
  N4: Part1.D8, LED4.anode
  N5: Part1.D9_PWM, J1.pin1
  N6: Part1.D10_PWM/SS, LED1.anode
  N7: Part1.D11_PWM/MOSI, LED3.anode
  N8: Part1.D12/MISO, LED2.anode
  N9: Part1.D13/SCK, LED5.anode
  GND: Part1.GND, U1.GND, S1.Pin_1, S1.Pin_2, S2.Pin_1, S2.Pin_2, R6.Pin_0, R7.Pin_0
  N10: LED1.cathode, R4.Pin_1
  N11: LED2.cathode, R2.Pin_1
  N12: LED3.cathode, R3.Pin_1
  N13: LED4.cathode, R5.Pin_1
  N14: LED5.cathode, R1.Pin_1
  N15: R1.Pin_0, R2.Pin_0, R3.Pin_0, R4.Pin_0, R5.Pin_0
