# Fritzing sketch id3238_quad_sensor_0 (saved by Fritzing 0.7.7b)
breadboards: 1

parts:
  U1 = LM 358 Dual Op-Amp [package="DIP8 [THT]"]
  R1 = Trimmer Potentiometer [maximum_resistance=10kΩ package=THT]
  R2 = Trimmer Potentiometer [maximum_resistance=10kΩ package=THT]
  U2 = LM 358 Dual Op-Amp [package="DIP8 [THT]"]
  R3 = Trimmer Potentiometer [maximum_resistance=10kΩ package=THT]
  R4 = Trimmer Potentiometer [maximum_resistance=10kΩ package=THT]
  in3 = male pin header, 3 pins [form="♂ (male)"]
  out4 = male pin header, 3 pins [form="♂ (male)"]
  out3 = male pin header, 3 pins [form="♂ (male)"]
  out2 = male pin header, 3 pins [form="♂ (male)"]
  out1 = male pin header, 3 pins [form="♂ (male)"]
  J1 = male pin header, 3 pins [form="♂ (male)"]
  in2 = male pin header, 3 pins [form="♂ (male)"]
  in1 = male pin header, 3 pins [form="♂ (male)"]
  in4 = male pin header, 3 pins [form="♂ (male)"]

nets:
  N1: U1.connector0, out1.pin3
  N2: U1.connector1, R1.wiper
  N3: U1.connector2, in1.pin3
  GND: U1.connector3, R1.leg1, R2.leg1, U2.connector3, R3.leg1, R4.leg1, in3.pin2, out4.pin2, out3.pin2, out2.pin2, out1.pin2, J1.pin2, in2.pin2, in1.pin2, in4.pin2
  N4: U1.connector4, in2.pin3
  N5: U1.connector5, R2.wiper
  N6: U1.connector6, out2.pin3
  5V: U1.connector7, R1.leg2, R2.leg2, U2.connector7, R3.leg2, R4.leg2, in3.pin1, out4.pin1, out3.pin1, out2.pin1, out1.pin1, J1.pin1, in2.pin1, in1.pin1, in4.pin1
  N7: U2.connector0, U2.connector2, in3.pin3, out3.pin3
  N8: U2.connector1, R3.wiper
  N9: U2.connector4, in4.pin3
  N10: U2.connector5, R4.wiper
  N11: U2.connector6, out4.pin3

notes:
  quad_sensor_comp.
  meng_inventor
