# Fritzing sketch id3239_LCDIMUSERial_0 (saved by Fritzing 0.7.12b)

parts:
  Arduino1 = Arduino
  Arduino2 = Arduino Mini
  LCD1 = LCD screen
  R1 = 27k Ω Resistor [package=THT]  # not connected

nets:
  GND: Arduino1.GND, Arduino2.GND, LCD1.VSS, LCD1.RS
  N1: Arduino1.D13, LCD1.E
  N2: Arduino1.D5, LCD1.DB4
  N3: Arduino1.D4, LCD1.DB5
  N4: Arduino1.D3, LCD1.DB6
  N5: Arduino1.D2, LCD1.DB7
  N6: Arduino1.D0RX, Arduino2.D0
  N7: Arduino1.RST, Arduino2.D7
  +5V: Arduino1.+5V, Arduino2.+5V, LCD1.VDD

notes:
  The BLK pin of IMU is grounded
  RX of IMU is unconnected since it is only transmitting data
  TX pin is used for printing on the serial monitor
