# Fritzing sketch id323_Raspberry_mpc3008_LM36DZ_temperature_0 (saved by Fritzing 0.8.3b)
breadboards: 1

parts:
  IC1 = MCP3008 [part_number=MCP3008]
  Raspberry_Pi_rev1 = Raspberry Pi rev2
  T1 = TMP36 Temperature Sensor [package="TO92 [THT]"]

nets:
  GND: IC1.connector9, IC1.connector14, Raspberry_Pi_rev1.GND, T1.GND
  N1: IC1.connector10, Raspberry_Pi_rev1.GPIO_8
  N2: IC1.connector11, Raspberry_Pi_rev1.GPIO_10
  N3: IC1.connector12, Raspberry_Pi_rev1.GPIO_9
  N4: IC1.connector13, Raspberry_Pi_rev1.GPIO_11
  N5: IC1.connector15, IC1.connector16, Raspberry_Pi_rev1.3V3, T1.+Vs
