# Fritzing sketch id3240_quadruped_0 (saved by Fritzing 0.9.2b)
breadboards: 1

parts:
  Parte1 = Arduino Uno (Rev3) - ICSP
  J1 = Basic Servo
  J2 = Infrared Proximity Sensor

nets:
  N1: Parte1.D2, J2.Vout
  N2: Parte1.D7, J1.pulse
  VCC: Parte1.5V, J1.vcc, J2.Vcc
  GND: Parte1.GND, J1.gnd, J2.GND
