# Fritzing sketch id3241_Quaduino_0 (saved by Fritzing 0.6.3b)
breadboards: 1

parts:
  USB = female pin header, 6 pins [form="♀ (female)"]
  CPU = atmega168 [package="DIP28 [THT]"]
  S1 = Pushbutton [package="[THT]"]
  16MHz = Crystal [frequency="16 Mhz" package=THT]
  C1 = Ceramic Capacitor [capacitance=100nF package="100 mil [THT, multilayer]"]
  C2 = Ceramic Capacitor [capacitance=100nF package="100 mil [THT, multilayer]"]
  R1 = Resistor [tolerance=±5% resistance=10k package=THT]
  C3 = Ceramic Capacitor [capacitance=100nF package="100 mil [THT, multilayer]"]
  LED = LED - 5mm [color="Red (633nm)" package="5 mm [THT]"]
  R2 = Resistor [tolerance=±5% resistance=220 package=THT]
  PWR = female pin header, 2 pins [form="♀ (female)"]
  J5 = female pin header, 14 pins [form="♀ (female)"]
  J6 = female pin header, 14 pins [form="♀ (female)"]

nets:
  N1: USB.pin1, CPU.Pin_8, CPU.Pin_22, S1.Pin_3, S1.Pin_4, C1.1, C2.1, LED.cathode, PWR.pin2, J5.pin7, J6.pin8
  N2: USB.pin3, CPU.Pin_7, CPU.Pin_20, R1.Pin_0, R2.Pin_1, PWR.pin1, J5.pin9, J6.pin7
  N3: USB.pin4, CPU.Pin_2, J6.pin2
  N4: USB.pin5, CPU.Pin_3, J6.pin3
  N5: USB.pin6, C3.0
  N6: CPU.Pin_1, S1.Pin_1, S1.Pin_2, R1.Pin_1, C3.1, J6.pin1
  N7: CPU.Pin_4, J6.pin4
  N8: CPU.Pin_5, J6.pin5
  N9: CPU.Pin_6, J6.pin6
  N10: CPU.Pin_9, 16MHz.pin_0, C1.0, J6.pin9
  N11: CPU.Pin_10, 16MHz.pin_1, C2.0, J6.pin10
  N12: CPU.Pin_11, J6.pin11
  N13: CPU.Pin_12, J6.pin12
  N14: CPU.Pin_13, J6.pin13
  N15: CPU.Pin_14, J6.pin14
  N16: CPU.Pin_15, J5.pin14
  N17: CPU.Pin_16, J5.pin13
  N18: CPU.Pin_17, J5.pin12
  N19: CPU.Pin_18, J5.pin11
  N20: CPU.Pin_19, J5.pin10
  N21: CPU.Pin_21, J5.pin8
  N22: CPU.Pin_23, J5.pin6
  N23: CPU.Pin_24, J5.pin5
  N24: CPU.Pin_25, J5.pin4
  N25: CPU.Pin_26, J5.pin3
  N26: CPU.Pin_27, J5.pin2
  N27: CPU.Pin_28, J5.pin1
  N28: LED.anode, R2.Pin_0
