# Fritzing sketch id3243_Quirbot_Example___Servo_0 (saved by Fritzing 0.8.7b)

parts:
  Part1 = Arduino Uno (Rev3)
  J1 = Basic Servo

nets:
  N1: Part1.D8, J1.pulse
  5V: Part1.5V, J1.vcc
  GND: Part1.GND, J1.gnd
