# Fritzing sketch id3244_Quiz_1.0.0_0 (saved by Fritzing 0.9.3b)
breadboards: 2
stripboards: 1

parts:
  Arduino_LCD = Arduino Uno (Rev3)
  Arduino_7_SEG = Arduino Uno (Rev3)
  LCD = LCD screen
  Bottone_Rosso = Pushbutton [package="[THT]"]
  R1 = Resistor [tolerance=±1% resistance=10k package=THT]
  Bottone_Giallo = Pushbutton [package="[THT]"]
  R2 = Resistor [tolerance=±1% resistance=10k package=THT]
  Piezo = Piezo Speaker
  DI1 = 7-Segment LED Display [package=THT]
  R3 = Resistor [tolerance=±1% resistance=330 package=THT]
  R4 = Resistor [tolerance=±1% resistance=330 package=THT]
  R5 = Resistor [tolerance=±1% resistance=330 package=THT]
  R6 = Resistor [tolerance=±1% resistance=330 package=THT]
  R8 = Resistor [tolerance=±1% resistance=330 package=THT]
  R9 = Resistor [tolerance=±1% resistance=330 package=THT]
  R10 = Resistor [tolerance=±1% resistance=330 package=THT]

nets:
  N1: Arduino_LCD.D8, LCD.E
  N2: Arduino_LCD.D9_PWM, LCD.V0
  N3: Arduino_LCD.D10_PWM/SS, LCD.DB4
  N4: Arduino_LCD.D11_PWM/MOSI, LCD.DB5
  N5: Arduino_LCD.D12/MISO, LCD.DB6
  N6: Arduino_LCD.D13/SCK, LCD.DB7
  N7: Arduino_LCD.D2, Bottone_Rosso.Pin_1, Bottone_Rosso.Pin_2, R1.Pin_0
  GND: Arduino_LCD.D3_PWM, Arduino_LCD.GND, LCD.VSS, LCD.LED-, R1.Pin_1, R2.Pin_0, Piezo.pin1, Piezo.pin2
  N8: Arduino_LCD.D4, Bottone_Giallo.Pin_1, Bottone_Giallo.Pin_2, R2.Pin_1
  N9: Arduino_LCD.D5_PWM, Arduino_7_SEG.D12/MISO
  N10: Arduino_LCD.D6_PWM, LCD.RS
  N11: Arduino_LCD.D7, LCD.R/W
  5V: Arduino_LCD.5V, LCD.VDD, LCD.LED+, Bottone_Rosso.Pin_3, Bottone_Rosso.Pin_4, Bottone_Giallo.Pin_3, Bottone_Giallo.Pin_4
  N12: Arduino_7_SEG.D8, R6.Pin_1
  N13: Arduino_7_SEG.D9_PWM, R5.Pin_1
  N14: Arduino_7_SEG.D10_PWM/SS, R4.Pin_1
  N15: Arduino_7_SEG.D11_PWM/MOSI, R3.Pin_1
  N16: Arduino_7_SEG.D5_PWM, R10.Pin_1
  N17: Arduino_7_SEG.D6_PWM, R9.Pin_1
  N18: Arduino_7_SEG.D7, R8.Pin_1
  N19: Arduino_7_SEG.GND, DI1.commAnode
  N20: DI1.cathodeE, R8.Pin_0
  N21: DI1.cathodeD, R9.Pin_0
  N22: DI1.cathodeC, R10.Pin_0
  N23: DI1.cathodeB, R6.Pin_0
  N24: DI1.cathodeA, R5.Pin_0
  N25: DI1.cathodeF, R4.Pin_0
  N26: DI1.cathodeG, R3.Pin_0
