# Fritzing sketch id3245_quiz_4_giocatori_0 (saved by Fritzing 0.7.4b)
breadboards: 1

parts:
  R1 = Trimmer Potentiometer [maximum_resistance=10kΩ package=THT]
  R2 = Trimmer Potentiometer [maximum_resistance=10kΩ package=THT]
  Arduino1 = Arduino
  7_Segment1 = 7 Segment Display
  S1 = Pushbutton [package="[THT]"]
  S2 = Pushbutton [package="[THT]"]
  S3 = Pushbutton [package="[THT]"]
  S4 = Pushbutton [package="[THT]"]
  R3 = Resistor [tolerance=±5% resistance=10k package=THT]
  R4 = Resistor [tolerance=±5% resistance=10k package=THT]
  R5 = Resistor [tolerance=±5% resistance=10k package=THT]
  R6 = Resistor [tolerance=±5% resistance=10k package=THT]
  LED2 = LED - 5mm [color="Green (570nm)" package="5 mm [THT]"]
  LED3 = LED - 5mm [color="Green (570nm)" package="5 mm [THT]"]
  LED4 = LED - 5mm [color="Green (570nm)" package="5 mm [THT]"]
  LED6 = LED - 5mm [color="Red (633nm)" package="5 mm [THT]"]
  LED5 = LED - 5mm [color="Green (570nm)" package="5 mm [THT]"]

nets:
  N1: R1.leg1, R2.leg1, Arduino1.GND, 7_Segment1.common_anode, R3.Pin_1, R4.Pin_1, R5.Pin_1, R6.Pin_1, LED2.cathode, LED3.cathode, LED4.cathode, LED6.cathode, LED5.cathode
  N2: R1.wiper, Arduino1.A0
  N3: R1.leg2, R2.leg2, Arduino1.+5V, S1.Pin_1, S1.Pin_2, S2.Pin_1, S2.Pin_2, S3.Pin_1, S3.Pin_2, S4.Pin_1, S4.Pin_2
  N4: R2.wiper, Arduino1.A1
  N5: Arduino1.D13, 7_Segment1.Segment_G
  N6: Arduino1.D12, 7_Segment1.Segment_F
  N7: Arduino1.D11, 7_Segment1.Segment_E
  N8: Arduino1.D10, 7_Segment1.Segment_D
  N9: Arduino1.D9, 7_Segment1.Segment_C
  N10: Arduino1.D8, 7_Segment1.Segment_B
  N11: Arduino1.D7, 7_Segment1.Segment_A
  N12: Arduino1.D6, LED6.anode
  N13: Arduino1.D5, LED5.anode
  N14: Arduino1.D4, LED4.anode
  N15: Arduino1.D3, LED3.anode
  N16: Arduino1.D2, LED2.anode
  N17: Arduino1.A2, S1.Pin_3, S1.Pin_4, R3.Pin_0
  N18: Arduino1.A3, S2.Pin_3, S2.Pin_4, R4.Pin_0
  N19: Arduino1.A4, S3.Pin_3, S3.Pin_4, R5.Pin_0
  N20: Arduino1.A5, S4.Pin_3, S4.Pin_4, R6.Pin_0
