# Fritzing sketch id3246_candlelight_0 (saved by Fritzing 0.9.3b)
circuit board: 8.46667cm x 5.64444cm
breadboards: 1

parts:
  Bauteil1 = Arduino Uno (Rev3)
  LED1 = LED - 3mm [color="Red (635nm)" package="3 mm [THT]"]
  LED3 = LED - 3mm [color="Green (555nm)" package="3 mm [THT]"]
  R1 = Resistor [tolerance=±5% resistance=1.5k package=THT]
  R2 = Resistor [tolerance=±5% resistance=1.5k package=THT]
  R3 = Resistor [tolerance=±5% resistance=1.5k package=THT]
  LED2 = LED - 3mm [color="Yellow (592nm)" package="3 mm [THT]"]

nets:
  N1: Bauteil1.D9_PWM, LED3.anode
  N2: Bauteil1.D10_PWM/SS, LED2.anode
  N3: Bauteil1.D11_PWM/MOSI, LED1.anode
  N4: Bauteil1.GND, R1.Pin_1, R2.Pin_1, R3.Pin_1
  N5: LED1.cathode, R1.Pin_0
  N6: LED3.cathode, R3.Pin_0
  N7: R2.Pin_0, LED2.cathode
