# Fritzing sketch id3247_comando_0 (saved by Fritzing 0.8.7b)

parts:
  Componente1 = Arduino Pro Mini v13
  J1 = female pin header, 4 pins [form="♀ (female)"]
  J2 = female pin header, 4 pins [form="♀ (female)"]
  J3 = male pin header, 2 pins [form="♂ (male)"]
  J4 = male pin header, 6 pins [form="♂ (male)"]
  J5 = male pin header, 6 pins [form="♂ (male)"]
  J6 = male pin header, 2 pins [form="♂ (male)"]
  J7 = male pin header, 2 pins [form="♂ (male)"]
  J8 = male pin header, 3 pins [form="♂ (male)"]
  J9 = male pin header, 3 pins [form="♂ (male)"]
  J10 = male pin header, 3 pins [form="♂ (male)"]
  J11 = male pin header, 3 pins [form="♂ (male)"]
  J12 = male pin header, 3 pins [form="♂ (male)"]
  J13 = male pin header, 3 pins [form="♂ (male)"]
  J14 = male pin header, 3 pins [form="♂ (male)"]
  J15 = male pin header, 3 pins [form="♂ (male)"]
  J16 = female pin header, 4 pins [form="♀ (female)"]
  J17 = male pin header, 2 pins [form="♂ (male)"]

nets:
  N1: Componente1.RAW, J6.pin2
  N2: Componente1.GND, J2.pin4, J4.pin1, J4.pin2, J4.pin3, J4.pin4, J4.pin5, J4.pin6, J7.pin1, J8.pin3, J9.pin3, J10.pin3, J11.pin3, J12.pin3, J13.pin3, J14.pin3, J15.pin3, J17.pin1
  N3: Componente1.VCC, J1.pin4, J8.pin1, J9.pin1, J10.pin1, J11.pin1, J12.pin1, J13.pin1, J14.pin1, J15.pin1
  N4: Componente1.A3, J8.pin2
  N5: Componente1.A2, J9.pin2
  N6: Componente1.A1, J10.pin2
  N7: Componente1.A0, J11.pin2
  N8: Componente1.D13/SCK, J2.pin2
  N9: Componente1.D12/MISO, J2.pin1
  N10: Componente1.D11_PWM/MOSI, J1.pin2
  N11: Componente1.D10_PWM/SS, J2.pin3
  N12: Componente1.D9_PWM, J1.pin3
  N13: Componente1.D8, J17.pin2
  N14: Componente1.D7, J5.pin1
  N15: Componente1.D6_PWM, J5.pin2
  N16: Componente1.D5_PWM, J5.pin3
  N17: Componente1.D4, J5.pin4
  N18: Componente1.D3_PWM, J5.pin5
  N19: Componente1.D2, J5.pin6
  N20: Componente1.D1/RX, J3.pin1
  N21: Componente1.D0/TX, J3.pin2
  N22: J6.pin1, J7.pin2
  N23: J12.pin2, J16.pin4
  N24: J13.pin2, J16.pin3
  N25: J14.pin2, J16.pin2
  N26: J15.pin2, J16.pin1

notes:
  - +
  Alimentazione
  Interruttore
  Stick 1
  Stick 2
  Stick 3
  Stick 4
  UART
  OUTPUT
  Switch 1
  Switch 2
  Switch 3
  Switch 4
  A7 A6 A5 A4
