# Fritzing sketch id3248_Galena_001_0 (saved by Fritzing 0.9.0b)
circuit board: 5.59826cm x 2.72613cm
breadboards: 1

parts:
  L1 = Inductor [package="400 mil [THT]"]
  L2 = Inductor [package="400 mil [THT]"]
  R1 = Resistor [tolerance=±5% resistance=220 package=THT]
  D2 = Rectifier Diode [part_number=1N4001 package="300 mil [THT]"]
  D4 = Rectifier Diode [part_number=1N4001 package="300 mil [THT]"]
  L3 = Inductor [package="400 mil [THT]"]
  L4 = Inductor [package="400 mil [THT]"]
  C1 = CAP_ADJ [package=ctz3]
  C2 = CAP_ADJ [package=ctz3]
  ANT1 = Antenna
  C3 = CAP_ADJ [package=ctz3]
  D1 = Rectifier Diode [part_number=1N4001 package="300 mil [THT]"]
  D3 = Rectifier Diode [part_number=1N4001 package="300 mil [THT]"]
  J1 = Piezo Speaker

nets:
  N1: L1.pin_0, ANT1.antenna_lead
  GND: L1.pin_1
  N2: L2.pin_0, L3.pin_0, C1.4, C3.4
  N3: L2.pin_1, C1.3, C2.4
  N4: R1.Pin_0, D1.cathode, D3.cathode, J1.pin1
  N5: R1.Pin_1, D2.anode, D4.anode, J1.pin2
  N6: D2.cathode, L4.pin_1, D1.anode
  N7: D4.cathode, L4.pin_0, D3.anode
  N8: L3.pin_1, C2.3, C3.3
