# Fritzing sketch id3249_ricevente_0 (saved by Fritzing 0.8.7b)

parts:
  Componente1 = Arduino Pro Mini v13
  J1 = female pin header, 4 pins [form="♀ (female)"]
  J2 = female pin header, 4 pins [form="♀ (female)"]
  J3 = male pin header, 3 pins [form="♂ (male)"]
  J6 = male pin header, 3 pins [form="♂ (male)"]
  J5 = male pin header, 3 pins [form="♂ (male)"]
  J4 = male pin header, 3 pins [form="♂ (male)"]
  J7 = male pin header, 3 pins [form="♂ (male)"]

nets:
  N1: Componente1.RAW, J3.pin2, J6.pin2, J5.pin2, J4.pin2, J7.pin2
  N2: Componente1.GND, J2.pin4, J3.pin1, J6.pin1, J5.pin1, J4.pin1, J7.pin1
  N3: Componente1.VCC, J1.pin4
  N4: Componente1.D13/SCK, J2.pin2
  N5: Componente1.D12/MISO, J2.pin1
  N6: Componente1.D11_PWM/MOSI, J1.pin2
  N7: Componente1.D10_PWM/SS, J7.pin3
  N8: Componente1.D9_PWM, J4.pin3
  N9: Componente1.D8, J1.pin3
  N10: Componente1.D7, J2.pin3
  N11: Componente1.D6_PWM, J5.pin3
  N12: Componente1.D5_PWM, J6.pin3
  N13: Componente1.D3_PWM, J3.pin3

notes:
  Stick 1
  Stick 2
  Stick 3
  Stick 4
  Stick 5
