# Fritzing sketch id3250_LED_Cube_3x3x3_0 (saved by Fritzing 0.9.2b)
circuit board: 16.9333cm x 5.64444cm
breadboards: 10

parts:
  LED1 = LED - 5mm [color="Red (633nm)" package="5 mm [THT]"]
  LED2 = LED - 5mm [color="Red (633nm)" package="5 mm [THT]"]
  LED3 = LED - 5mm [color="Red (633nm)" package="5 mm [THT]"]
  LED4 = LED - 5mm [color="Red (633nm)" package="5 mm [THT]"]
  LED5 = LED - 5mm [color="Red (633nm)" package="5 mm [THT]"]
  LED6 = LED - 5mm [color="Red (633nm)" package="5 mm [THT]"]
  LED7 = LED - 5mm [color="Red (633nm)" package="5 mm [THT]"]
  LED8 = LED - 5mm [color="Red (633nm)" package="5 mm [THT]"]
  LED9 = LED - 5mm [color="Red (633nm)" package="5 mm [THT]"]
  R5 = Resistor [tolerance=±5% resistance=100 package=THT]
  R3 = Resistor [tolerance=±5% resistance=100 package=THT]
  R8 = Resistor [tolerance=±5% resistance=100 package=THT]
  R6 = Resistor [tolerance=±5% resistance=100 package=THT]
  R2 = Resistor [tolerance=±5% resistance=100 package=THT]
  R9 = Resistor [tolerance=±5% resistance=100 package=THT]
  R7 = Resistor [tolerance=±5% resistance=100 package=THT]
  R1 = Resistor [tolerance=±5% resistance=100 package=THT]
  LED10 = LED - 5mm [color="Red (633nm)" package="5 mm [THT]"]
  LED11 = LED - 5mm [color="Red (633nm)" package="5 mm [THT]"]
  LED12 = LED - 5mm [color="Red (633nm)" package="5 mm [THT]"]
  LED13 = LED - 5mm [color="Red (633nm)" package="5 mm [THT]"]
  LED14 = LED - 5mm [color="Red (633nm)" package="5 mm [THT]"]
  LED15 = LED - 5mm [color="Red (633nm)" package="5 mm [THT]"]
  LED16 = LED - 5mm [color="Red (633nm)" package="5 mm [THT]"]
  LED17 = LED - 5mm [color="Red (633nm)" package="5 mm [THT]"]
  LED18 = LED - 5mm [color="Red (633nm)" package="5 mm [THT]"]
  LED19 = LED - 5mm [color="Red (633nm)" package="5 mm [THT]"]
  LED20 = LED - 5mm [color="Red (633nm)" package="5 mm [THT]"]
  LED21 = LED - 5mm [color="Red (633nm)" package="5 mm [THT]"]
  LED22 = LED - 5mm [color="Red (633nm)" package="5 mm [THT]"]
  LED23 = LED - 5mm [color="Red (633nm)" package="5 mm [THT]"]
  LED24 = LED - 5mm [color="Red (633nm)" package="5 mm [THT]"]
  LED25 = LED - 5mm [color="Red (633nm)" package="5 mm [THT]"]
  LED26 = LED - 5mm [color="Red (633nm)" package="5 mm [THT]"]
  LED27 = LED - 5mm [color="Red (633nm)" package="5 mm [THT]"]
  RS_3D_Cube = Arduino Uno (Rev3)
  R4 = Resistor [tolerance=±5% resistance=100 package=THT]

nets (from the schematic view):
  N1: LED1.cathode, LED2.cathode, LED3.cathode, LED4.cathode, LED5.cathode, LED6.cathode, LED7.cathode, LED8.cathode, LED9.cathode, RS_3D_Cube.D3_PWM
  N2: LED1.anode, R1.Pin_0, LED10.anode, LED19.anode
  N3: LED2.anode, R2.Pin_0, LED11.anode, LED20.anode
  N4: LED3.anode, R3.Pin_0, LED12.anode, LED21.anode
  N5: LED5.anode, R5.Pin_0, LED14.anode, LED23.anode
  N6: LED6.anode, R6.Pin_0, LED15.anode, LED24.anode
  N7: LED7.anode, R7.Pin_0, LED16.anode, LED25.anode
  N8: LED8.anode, R8.Pin_0, LED17.anode, LED26.anode
  N9: LED9.anode, R9.Pin_0, LED18.anode, LED27.anode
  N10: R5.Pin_1, RS_3D_Cube.D9_PWM
  N11: R3.Pin_1, RS_3D_Cube.D2
  N12: R8.Pin_1, RS_3D_Cube.D12/MISO
  N13: R6.Pin_1, RS_3D_Cube.D8
  N14: R2.Pin_1, RS_3D_Cube.D4
  N15: R9.Pin_1, RS_3D_Cube.D11_PWM/MOSI
  N16: R7.Pin_1, RS_3D_Cube.D13/SCK
  N17: R1.Pin_1, RS_3D_Cube.D7
  N18: LED10.cathode, LED11.cathode, LED12.cathode, LED13.cathode, LED14.cathode, LED15.cathode, LED16.cathode, LED17.cathode, LED18.cathode, RS_3D_Cube.D5_PWM
  N19: LED13.anode, LED22.anode, R4.Pin_0
  N20: LED19.cathode, LED20.cathode, LED21.cathode, LED22.cathode, LED23.cathode, LED24.cathode, LED25.cathode, LED26.cathode, LED27.cathode, RS_3D_Cube.D6_PWM
  N21: RS_3D_Cube.D10_PWM/SS, R4.Pin_1

notes:
  XYZ
  111
  211
  311
  211
  221
  231
  311
  321
  321
  112
  212
  312
  212
  222
  232
  312
  322
  322
  113
  213
  313
  213
  223
  233
  313
  323
  323
