# Fritzing sketch id3251_radio_0 (saved by Fritzing 0.9.0b)
circuit board: 8.46667cm x 5.64444cm
breadboards: 1

parts:
  Q1 = NPN-Transistor [package="TO92 [THT]"]
  Q2 = NPN-Transistor [package="TO92 [THT]"]
  R3 = Resistor [tolerance=±20% resistance=0 package=THT]
  L1 = Inductor [package="400 mil [THT]"]
  Q3 = PNP-Transistor [package="TO92 [THT]"]
  R5 = Resistor [tolerance=±20% resistance=0 package=THT]
  ANT1 = Antenna
  R6 = Resistor [tolerance=±5% resistance=220 package=THT]
  BAT1 = Battery Holders [package=battery-aa-kit]
  Audio_In = 2.5mm Audio Jack [package=stereojack2.5mm_specia_pogopins]
  LED1 = LED - 5mm [color="Red (633nm)" package="5 mm [THT]"]
  D1 = Zener Diode [part_number=1N4732A breakdown_voltage=3.6V package="300 mil [THT]"]
  D2 = Zener Diode [part_number=1N4732A breakdown_voltage=3.6V package="300 mil [THT]"]
  U1 = SWITCH_SPDT [package=kps-1290]
  L2 = Inductor [package="400 mil [THT]"]
  R7 = Resistor [tolerance=±20% resistance=0 package=THT]
  L3 = Inductor [package="400 mil [THT]"]
  C8 = Capacitor [package=cap-pth-small2]
  C9 = Electrolytic Capacitor [capacitance=1µF package="100 mil [THT, electrolytic]"]
  C10 = Capacitor [package=cap-pth-small2]
  C11 = Capacitor [package=cap-pth-small2]
  C12 = Capacitor [package=cap-pth-small2]
  C13 = Capacitor [package=cap-pth-small2]
  C14 = Capacitor [package=cap-pth-small2]

nets (from the schematic view):
  GND: Q1.E, R3.Pin_0, R5.Pin_0, BAT1.-, Audio_In.SLEEVE, U1.S, C9.-, C10.2, C13.2
  N1: Q1.B, D1.anode, C11.2
  N2: Q1.C, Q2.B, R6.Pin_0, D1.cathode, C13.1
  N3: Q2.E, R3.Pin_1, C12.2
  N4: Q2.C, L1.pin_0, C8.2, C12.1
  N5: L1.pin_1, Q3.E, LED1.anode, C8.1, C14.1
  N6: Q3.B, L2.pin_1, C14.2
  N7: Q3.C, L3.pin_1
  N8: R5.Pin_1, L3.pin_0
  N9: ANT1.antenna_lead, R7.Pin_0
  N10: R6.Pin_1, D2.cathode, C9.+, C10.1
  N11: BAT1.+, U1.O
  N12: Audio_In.LEFT, Audio_In.RIGHT, D2.anode, C11.1
  N13: LED1.cathode, U1.P
  N14: L2.pin_0, R7.Pin_1
