# Fritzing sketch id3252_RadioLab_Temperature_Board_0 (saved by Fritzing 0.7.12b)
breadboards: 1

parts:
  R1 = Resistor [tolerance=±5% resistance=330 package=THT]
  R2 = Resistor [tolerance=±5% resistance=330 package=THT]
  R3 = Resistor [tolerance=±5% resistance=330 package=THT]
  R4 = Resistor [tolerance=±5% resistance=330 package=THT]
  R5 = Resistor [tolerance=±5% resistance=330 package=THT]
  R6 = Resistor [tolerance=±5% resistance=330 package=THT]
  R7 = Resistor [tolerance=±5% resistance=330 package=THT]
  R8 = Resistor [tolerance=±5% resistance=330 package=THT]
  R9 = Resistor [tolerance=±5% resistance=330 package=THT]
  R10 = Resistor [tolerance=±5% resistance=10k package=THT]
  R11 = Resistor [tolerance=±5% resistance=10k package=THT]
  R12 = Resistor [tolerance=±5% resistance=10k package=THT]
  R13 = Resistor [tolerance=±5% resistance=10k package=THT]
  R14 = Resistor [tolerance=±5% resistance=10k package=THT]
  LED1 = LED - 5mm [color="Green (565nm)" package="5 mm [THT]"]
  LED2 = LED - 5mm [color="Green (565nm)" package="5 mm [THT]"]
  LED3 = LED - 5mm [color="Green (565nm)" package="5 mm [THT]"]
  LED4 = LED - 5mm [color="Green (565nm)" package="5 mm [THT]"]
  LED5 = LED - 5mm [color="Green (565nm)" package="5 mm [THT]"]
  LED6 = LED - 5mm [color="Green (565nm)" package="5 mm [THT]"]
  LED7 = LED - 5mm [color="Green (565nm)" package="5 mm [THT]"]
  LED8 = LED - 5mm [color="Green (565nm)" package="5 mm [THT]"]
  LED9 = LED - 5mm [color="Green (565nm)" package="5 mm [THT]"]
  Arduino1 = Arduino
  J1 = female pin header, 2 pins [form="♀ (female)"]

nets:
  N1: R1.Pin_0, R2.Pin_0, R3.Pin_0, R4.Pin_0, R5.Pin_0, R6.Pin_0, R7.Pin_0, R8.Pin_0, R9.Pin_0, R10.Pin_0, Arduino1.GND
  N2: R1.Pin_1, LED1.cathode
  N3: R2.Pin_1, LED2.cathode
  N4: R3.Pin_1, LED3.cathode
  N5: R4.Pin_1, LED4.cathode
  N6: R5.Pin_1, LED5.cathode
  N7: R6.Pin_1, LED6.cathode
  N8: R7.Pin_1, LED7.cathode
  N9: R8.Pin_1, LED8.cathode
  N10: R9.Pin_1, LED9.cathode
  N11: R10.Pin_1, R11.Pin_1
  N12: R11.Pin_0, R12.Pin_1
  N13: R12.Pin_0, R13.Pin_1
  N14: R13.Pin_0, R14.Pin_0, R14.Pin_1, Arduino1.A0, J1.pin1
  N15: LED1.anode, Arduino1.D2
  N16: LED2.anode, Arduino1.D3
  N17: LED3.anode, Arduino1.D4
  N18: LED4.anode, Arduino1.D5
  N19: LED5.anode, Arduino1.D6
  N20: LED6.anode, Arduino1.D7
  N21: LED7.anode, Arduino1.D8
  N22: LED8.anode, Arduino1.D9
  N23: LED9.anode, Arduino1.D10
  N24: Arduino1.+5V, J1.pin2
