# Fritzing sketch id3253_7_segment_led_0 (saved by Fritzing 0.7.10b)
breadboards: 1

parts:
  7_Segment1 = 7 Segment Display
  Arduino1 = Arduino
  R1 = Resistor [tolerance=±5% resistance=1.5k package=THT]
  R2 = Resistor [tolerance=±5% resistance=1.5k package=THT]

nets:
  N1: 7_Segment1.Segment_G, Arduino1.D2
  N2: 7_Segment1.Segment_F, R1.Pin_1
  N3: 7_Segment1.Segment_E, Arduino1.D3
  N4: 7_Segment1.Segment_D, Arduino1.D4
  N5: 7_Segment1.Segment_DP, Arduino1.D5
  N6: 7_Segment1.Segment_C, R2.Pin_0
  N7: 7_Segment1.Segment_B, Arduino1.D6
  N8: 7_Segment1.Segment_A, Arduino1.D7
  N9: Arduino1.GND, R1.Pin_0, R2.Pin_1

notes:
  RadioShack 7 Segment LED
  PN: 276-0075
  Segment Arduino
  1 2
  2 8
  4 GND
  6 3
  7 4
  8 5
  9 N/A
  12 GND
  13 6
  14 7
