# Fritzing sketch id3254_FYP_SCHEMATIC_DESIGN_0 (saved by Fritzing 0.9.2b)
breadboards: 1

parts:
  Part1 = Lilypad Arduino Board
  LED1 = RGB LED (com. cathode, rbg) [package="5 mm [THT]"]
  R1 = Photocell (LDR) [package=THT]
  U1 = LCD-16X2 [package=lcd-16x2_noholes]
  R2 = Resistor [tolerance=±5% resistance=220 package="0805 [SMD]"]
  R3 = Resistor [tolerance=±5% resistance=220 package="0805 [SMD]"]

nets:
  N1: Part1.GND, LED1.common_cathode, R1.pin_0, R2.Pin_0, R2.Pin_1, R3.Pin_0, R3.Pin_1
  N2: Part1.A0, R1.pin_1
  N3: Part1.D8, U1.DB6
  N4: Part1.D9, U1.DB5
  N5: Part1.D10, U1.DB4
  N6: Part1.MOSI/D11, U1.E
  N7: Part1.MISO/D12, U1.RS
  N8: Part1.D5, LED1.green_anode
  N9: Part1.D4, LED1.blue_anode
  N10: Part1.D3, LED1.red_anode
  N11: Part1.D7, U1.DB7
