# Fritzing sketch id3255_RAKS_CIRCUIT_DESIGN_0 (saved by Fritzing 0.7.12b)
breadboards: 1

parts:
  U1 = Arduino Mega
  J1 = Basic Servo
  J2 = Basic Servo
  J3 = Basic Servo
  J4 = Basic Servo
  J5 = Basic Servo

nets:
  N1: U1.D10, J5.pulse
  N2: U1.D6, J4.pulse
  N3: U1.D5, J3.pulse
  N4: U1.D4, J2.pulse
  N5: U1.D3, J1.pulse
  VCC: U1.+5V, J1.vcc, J2.vcc, J3.vcc, J4.vcc, J5.vcc
  GND: U1.GND, J1.gnd, J2.gnd, J3.gnd, J4.gnd, J5.gnd
