# Fritzing sketch id3256_Random_RGB_Led_v2_0 (saved by Fritzing 0.7.10b)
breadboards: 1

parts:
  Arduino1 = Arduino
  R1 = Resistor [tolerance=±5% resistance=220 package=THT]
  LED1 = RGB LED (com. anode, rbg) [package="5 mm [THT]"]
  R2 = Resistor [tolerance=±5% resistance=220 package=THT]
  R3 = Resistor [tolerance=±5% resistance=220 package=THT]
  S1 = Pushbutton [package="[THT]"]
  R4 = Resistor [tolerance=±5% resistance=10k package=THT]

nets:
  N1: Arduino1.D11, R1.Pin_0
  N2: Arduino1.D10, R2.Pin_0
  N3: Arduino1.D9, R3.Pin_0
  N4: Arduino1.D2, S1.Pin_1, S1.Pin_2, R4.Pin_1
  N5: Arduino1.+5V, S1.Pin_3, S1.Pin_4
  N6: Arduino1.GND, LED1.common_anode, R4.Pin_0
  N7: R1.Pin_1, LED1.red_cathode
  N8: LED1.blue_cathode, R2.Pin_1
  N9: LED1.green_cathode, R3.Pin_1
