# Fritzing sketch id3257_433MHz_Repeater_0 (saved by Fritzing 0.9.3b)
circuit board: 4.8775cm x 5.05312cm

parts:
  TX = RF-LINK_TX [package=rf-link_tx]
  RX = RF-LINK_RX [package=rf-link_rx]
  ANT1 = Antenna
  ANT2 = Antenna
  Arduino_Nano = Arduino Nano (Rev3.0)

nets:
  N1: TX.ANT, ANT2.antenna_lead
  N2: TX.DATA, Arduino_Nano.D5
  GND: TX.GND, RX.GND, Arduino_Nano.GND
  +5V: TX.+5V, RX.+5V, Arduino_Nano.5V
  N3: RX.DATA, Arduino_Nano.D2
  N4: RX.ANT, ANT1.antenna_lead
