# Fritzing sketch id3258_Rainbird_0 (saved by Fritzing 0.9.3b)
circuit board: 8.46667cm x 5.64444cm
breadboards: 1

parts:
  Bauteil1 = Arduino Nano (Rev3.0)
  U1 = LIPO-2000mAh [package=lipo-2000]
  WeMos_D1_Mini_Relay_Shield_V1 = WeMos D1 Mini Relay Shield V2
  WeMos_D1_Mini_Relay_Shield_V2 = WeMos D1 Mini Relay Shield V2

nets:
  N1: Bauteil1.GND, U1.-
  N2: Bauteil1.D3, WeMos_D1_Mini_Relay_Shield_V2.D3
  N3: Bauteil1.D4, WeMos_D1_Mini_Relay_Shield_V1.D4
  N4: Bauteil1.VIN, U1.+
  5V: Bauteil1.5V, WeMos_D1_Mini_Relay_Shield_V1.5V, WeMos_D1_Mini_Relay_Shield_V2.5V
  N5: WeMos_D1_Mini_Relay_Shield_V1.G, WeMos_D1_Mini_Relay_Shield_V2.G
