# Fritzing sketch id325_analogReadHelp_0 (saved by Fritzing 0.9.2b)
breadboards: 1

parts:
  Arduino1 = Arduino Uno (Rev3)
  R1 = Resistor [tolerance=±5% resistance=10k package=THT]
  R2 = Resistor [tolerance=±20% resistance=5.4k package=THT]
  VCC1 = Battery block 9V
  Q1 = NPN-Transistor [package="TO92 [THT]"]
  R3 = Resistor [tolerance=±5% resistance=220 package=THT]
  L1 = Inductor [package="400 mil [THT]"]
  D1 = Rectifier Diode [part_number=1N4001 package="300 mil [THT]"]

nets:
  N1: Arduino1.A2, R1.Pin_1, R2.Pin_0
  N2: Arduino1.D9_PWM, R3.Pin_1
  N3: Arduino1.5V, L1.pin_0, D1.cathode
  N4: Arduino1.GND, R2.Pin_1, VCC1.-, Q1.C
  N5: R1.Pin_0, VCC1.+
  N6: Q1.E, L1.pin_1, D1.anode
  N7: Q1.B, R3.Pin_0

notes:
  BLINK
