# Fritzing sketch id3260_Raspberry_8CH_Relay_Powerboard_0 (saved by Fritzing 0.9.2b)
circuit board: 4.41925cm x 3.64874cm

parts:
  Q1 = NPN-Transistor [package="TO92 [THT]"]
  J1 = female pin header, 10 pins [form="♀ (female)"]
  J2 = female pin header, 10 pins [form="♀ (female)"]
  R1 = Resistor [tolerance=±5% resistance=10k package=THT]
  R2 = Resistor [tolerance=±5% resistance=2.2k package=THT]
  Q2 = NPN-Transistor [package="TO92 [THT]"]
  R3 = Resistor [tolerance=±5% resistance=10k package=THT]
  R4 = Resistor [tolerance=±5% resistance=2.2k package=THT]
  Q3 = NPN-Transistor [package="TO92 [THT]"]
  R5 = Resistor [tolerance=±5% resistance=10k package=THT]
  R6 = Resistor [tolerance=±5% resistance=2.2k package=THT]
  Q4 = NPN-Transistor [package="TO92 [THT]"]
  R7 = Resistor [tolerance=±5% resistance=10k package=THT]
  R8 = Resistor [tolerance=±5% resistance=2.2k package=THT]
  Q5 = NPN-Transistor [package="TO92 [THT]"]
  R9 = Resistor [tolerance=±5% resistance=10k package=THT]
  R10 = Resistor [tolerance=±5% resistance=2.2k package=THT]
  Q6 = NPN-Transistor [package="TO92 [THT]"]
  R11 = Resistor [tolerance=±5% resistance=10k package=THT]
  R12 = Resistor [tolerance=±5% resistance=2.2k package=THT]
  Q7 = NPN-Transistor [package="TO92 [THT]"]
  R13 = Resistor [tolerance=±5% resistance=10k package=THT]
  R14 = Resistor [tolerance=±5% resistance=2.2k package=THT]
  Q8 = NPN-Transistor [package="TO92 [THT]"]
  R15 = Resistor [tolerance=±5% resistance=10k package=THT]
  R16 = Resistor [tolerance=±5% resistance=2.2k package=THT]

nets:
  N1: Q1.E, J1.pin1, Q2.E, Q3.E, Q4.E, Q5.E, Q6.E, Q7.E, Q8.E
  N2: Q1.B, R2.Pin_0
  N3: Q1.C, J1.pin2
  N4: J1.pin3, Q2.C
  N5: J1.pin4, Q3.C
  N6: J1.pin5, Q4.C
  N7: J1.pin6, Q5.C
  N8: J1.pin7, Q6.C
  N9: J1.pin8, Q7.C
  N10: J1.pin9, Q8.C
  N11: J1.pin10, J2.pin10
  N12: J2.pin1, R1.Pin_1, R3.Pin_1, R5.Pin_1, R7.Pin_1, R9.Pin_1, R11.Pin_1, R13.Pin_1, R15.Pin_1
  N13: J2.pin2, R1.Pin_0, R2.Pin_1
  N14: J2.pin3, R3.Pin_0, R4.Pin_1
  N15: J2.pin4, R5.Pin_0, R6.Pin_1
  N16: J2.pin5, R7.Pin_0, R8.Pin_1
  N17: J2.pin6, R9.Pin_0, R10.Pin_1
  N18: J2.pin7, R11.Pin_0, R12.Pin_1
  N19: J2.pin8, R13.Pin_0, R14.Pin_1
  N20: J2.pin9, R15.Pin_0, R16.Pin_1
  N21: Q2.B, R4.Pin_0
  N22: Q3.B, R6.Pin_0
  N23: Q4.B, R8.Pin_0
  N24: Q5.B, R10.Pin_0
  N25: Q6.B, R12.Pin_0
  N26: Q7.B, R14.Pin_0
  N27: Q8.B, R16.Pin_0

notes:
  5V
  GND
  10kΩ
  2.2kΩ
  Relay 1-8
  GPIO 1-8
  5Vin
  5Vout
  NPN
