# Fritzing sketch id3262_Raspberry_Beret_0 (saved by Fritzing 0.9.3b)

parts:
  Raspberry_Pi_Zero1 = Raspberry Pi Zero
  J1 = Piezo Speaker
  LED1 = Adafruit_FLORA_RGB_Smart_Pixel
  LED2 = Adafruit_FLORA_RGB_Smart_Pixel
  LED3 = Adafruit_FLORA_RGB_Smart_Pixel
  VCC1 = 4 x AAA Battery Mount

nets:
  N1: Raspberry_Pi_Zero1.GPIO22, J1.pin2
  N2: Raspberry_Pi_Zero1.GND, J1.pin1, LED1.connector3, LED2.connector3, LED3.connector3, VCC1.-
  N3: Raspberry_Pi_Zero1.GPIO18, LED1.connector2
  N4: LED1.connector1, LED2.connector1, LED3.connector1, VCC1.+
  N5: LED1.connector4, LED2.connector2
  N6: LED2.connector4, LED3.connector2
