# Fritzing sketch id3264_ELV_Wetter_0 (saved by Fritzing 0.9.2b)
circuit board: 3.55649cm x 3.01292cm
breadboards: 1

parts:
  J1 = double row female pin header, 26 pins [form="♀ (female)"]
  J2 = female pin header, 4 pins [form="♀ (female)"]  # not connected
  J3 = female pin header, 4 pins [form="♀ (female)"]
  J4 = female pin header, 4 pins [form="♀ (female)"]

nets:
  N1: J1.pin9, J3.pin3
  N2: J1.pin10, J3.pin2
  N3: J1.pin14, J3.pin4, J4.pin4
  N4: J1.pin15, J4.pin1
  N5: J1.pin16, J4.pin2
  N6: J1.pin18, J3.pin1, J4.pin3
