# Fritzing sketch id3265_raspberry_hc_sr04_experiment_pwmled_0 (saved by Fritzing 0.9.2b)
breadboards: 1

parts:
  Raspberry_Pi1 = Raspberry Pi B+
  R1 = Resistor [tolerance=±5% resistance=1k package=THT]
  R2 = Resistor [tolerance=±5% resistance=1k package=THT]
  LED1 = LED - 5mm [color="Red (633nm)" package="5 mm [THT]"]

nets:
  N1: Raspberry_Pi1.GPIO17, R1.Pin_1
  N2: Raspberry_Pi1.GPIO13, LED1.anode
  N3: Raspberry_Pi1.GND, R2.Pin_1
  N4: R2.Pin_0, LED1.cathode

notes:
  import RPi.GPIO as GPIO
  import time
  from gpiozero import LED,PWMLED
  GPIO.setmode(GPIO.BCM)
  GPIO.setwarnings(False)
  #HC-SR04
  pinTrigger = 4
  pinEcho = 17
  #LEDs
  led_1 = PWMLED(13)
  led_2 = LED(19)
  led_3 = LED(26)
  GPIO.setup(pinTrigger, GPIO.OUT)
  GPIO.setup(pinEcho, GPIO.IN)
  try:
  while True:
  GPIO.output(pinTrigger, False)
  time.sleep(0.5)
  # Send 10us pulse to trigger
  GPIO.output(pinTrigger, True)
  time.sleep(0.00001)
  GPIO.output(pinTrigger, False)
  StartTime = time.time()
  # The start time is reset until the Echo pin is taken high (==1)
  while GPIO.input(pinEcho) == 0:
  StartTime = time.time()
  # Stop when the Echo pin is no longer high - the end time
  while GPIO.input(pinEcho) == 1:
  StopTime = time.time()
  # If the sensor is too close to an object, the Pi cannot
  # see the echo quickly enough, so it has to detect that
  # problem and say what has happened
  if StopTime-StartTime >= 0.04:
  print("Hold on there! You're too close for me to see.")
  StopTime = StartTime
  break
  # Calculate pulse length
  ElapsedTime = StopTime - StartTime
  # Distance pulse travelled in that time is
  # time multiplied by the speed of sound (cm/s)
  Distance = ElapsedTime * 34326
  # That was the distance there and back so halve the value
  Distance = Distance / 2
  print("Distance : %.1f" % Distance)
  # if Distance < 20 :
  # led_1.on()
  # elif Distance < 100 :
  # led_1.on()
  # led_2.on()
  # else :
  # led_1.on()
  # led_2.on()
  # led_3.on()
  led_1.blink(on_time=Distance/100, off_time=Distance/100)
  time.sleep(0.5)
  # led_1.off()
  led_2.off()
  led_3.off()
  except KeyboardInterrupt:
  print('EXIT')
  except:
  print('ERROR')
  finally:
  GPIO.cleanup()
