# Fritzing sketch id3266_UD02C2.7_005_Padlock_0 (saved by Fritzing 0.9.3b)
breadboards: 1

parts:
  Raspberry_Pi1 = Raspberry Pi 2
  LED1 = LED - 5mm [color="Red (633nm)" package="5 mm [THT]"]
  S1 = Pushbutton [package="[THT]"]
  LED2 = LED - 5mm [color="Red (633nm)" package="5 mm [THT]"]
  R2 = Resistor [tolerance=±5% resistance=330 package=THT]
  S2 = Pushbutton [package="[THT]"]
  LED3 = LED - 5mm [color="Red (633nm)" package="5 mm [THT]"]
  R3 = Resistor [tolerance=±5% resistance=330 package=THT]
  S3 = Pushbutton [package="[THT]"]
  LED4 = LED - 5mm [color="Red (633nm)" package="5 mm [THT]"]
  R4 = Resistor [tolerance=±5% resistance=330 package=THT]
  S4 = Pushbutton [package="[THT]"]
  LED5 = RGB LED (com. anode, rbg) [package="5 mm [THT]"]  # not connected
  J1 = Piezo Speaker
  R5 = Resistor [tolerance=±5% resistance=330 package=THT]
  R6 = Resistor [tolerance=±5% resistance=330 package=THT]
  R7 = Resistor [tolerance=±5% resistance=330 package=THT]
  R1 = Resistor [tolerance=±5% resistance=330 package=THT]

nets:
  N1: Raspberry_Pi1.GPIO17, J1.pin2
  N2: Raspberry_Pi1.GPIO13, R7.Pin_1
  N3: Raspberry_Pi1.GPIO19, R6.Pin_1
  N4: Raspberry_Pi1.GPIO26, R5.Pin_1
  N5: Raspberry_Pi1.GPIO21, LED4.anode
  N6: Raspberry_Pi1.GPIO20, LED3.anode
  N7: Raspberry_Pi1.GPIO16, LED2.anode
  N8: Raspberry_Pi1.GPIO12, LED1.anode
  N9: Raspberry_Pi1.GPIO7, S4.Pin_1, S4.Pin_2
  N10: Raspberry_Pi1.GPIO8, S3.Pin_1, S3.Pin_2
  N11: Raspberry_Pi1.GPIO25, S2.Pin_1, S2.Pin_2
  N12: Raspberry_Pi1.GPIO24, S1.Pin_1, S1.Pin_2
  N13: Raspberry_Pi1.GND, R2.Pin_1, R3.Pin_1, R4.Pin_1, J1.pin1, R1.Pin_1
  N14: Raspberry_Pi1.5V, S1.Pin_3, S1.Pin_4, S2.Pin_3, S2.Pin_4, S3.Pin_3, S3.Pin_4, S4.Pin_3, S4.Pin_4
  N15: LED1.cathode, R1.Pin_0
  N16: LED2.cathode, R2.Pin_0
  N17: LED3.cathode, R3.Pin_0
  N18: LED4.cathode, R4.Pin_0
