# Fritzing sketch id3268_LCD_with_contrast_control_0 (saved by Fritzing 0.7.7b)
breadboards: 1

parts:
  Raspberry_Pi1 = Raspberry_Pi__Model_B
  LCD1 = LCD screen
  R1 = Resistor [tolerance=±5% resistance=470 package=THT]
  R2 = Trimmer Potentiometer [maximum_resistance=10kΩ package=THT]

nets:
  N1: Raspberry_Pi1.connector2, LCD1.VDD, R1.Pin_0, R2.leg2
  N2: Raspberry_Pi1.connector6, LCD1.VSS, LCD1.R/W, LCD1.LED-, R2.leg1
  N3: Raspberry_Pi1.connector12, LCD1.DB7
  N4: Raspberry_Pi1.connector16, LCD1.DB6
  N5: Raspberry_Pi1.connector18, LCD1.DB5
  N6: Raspberry_Pi1.connector22, LCD1.DB4
  N7: Raspberry_Pi1.connector24, LCD1.E
  N8: Raspberry_Pi1.connector26, LCD1.RS
  N9: LCD1.V0, R2.wiper
  N10: LCD1.LED+, R1.Pin_1

notes:
  Raspberry Pi driving a 16x2 LCD module with backlight
  10k trimming potentiometer controlling contrast (Pin 3)
  470ohm fixed resistor between pins 15 & 16
