# Fritzing sketch id3269_raspberrypi2_ta7291p_dcmotor01_0 (saved by Fritzing 0.9.2b)
breadboards: 1

parts:
  Raspberry_Pi1 = Raspberry Pi 2
  U1 = TA7291P
  VCC1 = Battery
  M1 = DC Motor

nets:
  N1: Raspberry_Pi1.GND, VCC1.-
  N2: U1.connector2, M1.pin_2
