# Fritzing sketch id3270_raspberrypi_and_esp_wroom_02_0 (saved by Fritzing 0.9.2b)
breadboards: 1

parts:
  R1 = Resistor [tolerance=±5% resistance=10k package=THT]
  R2 = Resistor [tolerance=±5% resistance=10k package=THT]
  R3 = Resistor [tolerance=±5% resistance=10k package=THT]
  R4 = Resistor [tolerance=±5% resistance=10k package=THT]
  Raspberry_Pi_A1 = Raspberry Pi A
  U1 = mystery part, 18 pins [chip_label="ESP-WROOM-02 (DIP)"]
  U2 = mystery part, 3 pins [chip_label=?]
  C1 = Electrolytic Capacitor [capacitance=10µF package="100 mil [THT, electrolytic]"]
  C2 = Ceramic Capacitor [capacitance=100nF package="1206 [SMD, multilayer]"]

nets:
  N1: R1.Pin_0, U1.pin2
  N2: R1.Pin_1, R3.Pin_1, R4.Pin_0, U1.pin1, U2.pin3, C1.+
  N3: R2.Pin_0, U1.pin6
  N4: R2.Pin_1, Raspberry_Pi_A1.GND, U1.pin8, U1.pin9, U1.pin13, U1.pin18, U2.pin2, C1.-, C2.1
  N5: R3.Pin_0, U1.pin7
  N6: R4.Pin_1, U1.pin15
  N7: Raspberry_Pi_A1.5V, U2.pin1, C2.0
  N8: Raspberry_Pi_A1.GPIO_14, U1.pin12
  N9: Raspberry_Pi_A1.GPIO_15, U1.pin11
