# Fritzing sketch id3271_Raspberry_pi_Battery_circuit_0 (saved by Fritzing 0.9.3b)
stripboards: 1

parts:
  BAT1 = Battery Holders [package=lipo-1100mAh]
  BAT2 = Battery Holders [package=lipo-1100mAh]
  BAT3 = Battery Holders [package=lipo-1100mAh]
  BAT4 = Battery Holders [package=lipo-1100mAh]
  R2 = Resistor [tolerance=±5% resistance=220 package="2512 [SMD]"]
  R3 = Resistor [tolerance=±5% resistance=220 package="2512 [SMD]"]
  R4 = Resistor [tolerance=±5% resistance=220 package="2512 [SMD]"]
  R5 = Resistor [tolerance=±5% resistance=220 package="2512 [SMD]"]
  U1 = SWITCH_SPDT [package=kps-1290]
  U2 = Transformer [package=transformer_smd]
  Raspberry_Pi_Zero1 = Raspberry Pi Zero  # not connected
  Part1 = Power Cell LiPo Charger/Booster  # not connected

nets:
  N1: BAT1.+, R3.Pin_1
  N2: BAT1.-, BAT2.-, BAT3.-, BAT4.-, U2.1
  N3: BAT2.+, R2.Pin_1
  N4: BAT3.+, R4.Pin_1
  N5: BAT4.+, R5.Pin_1
  N6: R2.Pin_0, R3.Pin_0, R4.Pin_0, R5.Pin_0, U1.P
  N7: U1.O, U2.2
