# Fritzing sketch id3272_23017_0 (saved by Fritzing 0.7.11b)
breadboards: 1

parts:
  IC1 = MCP23017_I2C_I_O_Expander
  RaspberryPi1 = Raspberry_Pi_Model_B

nets:
  N1: IC1.connector9, IC1.connector13, IC1.connector18, RaspberryPi1.connector1, RaspberryPi1.connector3
  N2: IC1.connector10, IC1.connector15, IC1.connector16, IC1.connector17, RaspberryPi1.connector6
  N3: IC1.connector12, RaspberryPi1.connector5
