# Fritzing sketch id3273_connected_cage_0 (saved by Fritzing 0.9.3b)
breadboards: 1

parts:
  J1 = Basic Servo
  R1 = Resistor [tolerance=±5% resistance=470 package="0805 [SMD]"]
  R2 = Resistor [tolerance=±5% resistance=470 package="0805 [SMD]"]
  S2 = Momentary Switch [package=ksa_sealed_tac_switch]
  S3 = Momentary Switch [package=ksa_sealed_tac_switch]
  R3 = Resistor [tolerance=±5% resistance=220 package="0805 [SMD]"]
  R4 = Resistor [tolerance=±5% resistance=220 package="0805 [SMD]"]
  LED1 = LED - 5mm [color="Yellow (592nm)" package="5 mm [THT]"]
  Raspberry_Pi_1 = Raspberry Pi 2

nets:
  GND: J1.gnd, S2.3, S2.4, S3.3, S3.4, LED1.cathode, Raspberry_Pi_1.GND
  VCC: J1.vcc, Raspberry_Pi_1.5V
  N1: J1.pulse, Raspberry_Pi_1.GPIO18
  N2: R1.Pin_0, S3.1, Raspberry_Pi_1.GPIO9
  3V3: R1.Pin_1, R2.Pin_1, Raspberry_Pi_1.3v3, Raspberry_Pi_1.3V3
  N3: R2.Pin_0, S2.1, Raspberry_Pi_1.GPIO25
  N4: S2.2, R4.Pin_0, LED1.anode
  N5: S3.2, R3.Pin_0
  N6: R3.Pin_1, Raspberry_Pi_1.GPIO23
  N7: R4.Pin_1, Raspberry_Pi_1.GPIO22
