# Fritzing sketch id3274_delay_on_0 (saved by Fritzing 0.9.3b)
circuit board: 2.53227cm x 3.07707cm
breadboards: 1

parts:
  555 = 555 Timer [package="DIP8 [THT]"]
  R1 = Resistor [tolerance=±5% resistance=220 package=THT]
  C2 = Ceramic Capacitor [capacitance=100nF package="100 mil [THT, multilayer]"]
  DELAYED_USB_POWER = USB Connectors [package=usb-a-h]
  D1 = Rectifier Diode [part_number=1N4001 package="300 mil [THT]"]
  C1 = Electrolytic Capacitor [capacitance=2.2µF voltage=16V package="200 mil [THT, electrolytic]"]
  Q1 = npn-Powertransistor [package="TO220 [THT]"]
  INPUT_POWER = Screw terminal - 2 pins [package=THT]
  R2 = Resistor [tolerance=±5% resistance=220 package=THT]

nets:
  N1: 555.Ground, R1.Pin_0, C2.1, D1.anode, Q1.emitter, INPUT_POWER.pin2
  N2: 555.Trigger, 555.Threshold, R1.Pin_1, D1.cathode, C1.-
  N3: 555.Output, R2.Pin_0
  N4: 555.Reset, 555.Vcc_Supply_Voltage, DELAYED_USB_POWER.VBUS, C1.+, INPUT_POWER.pin1
  N5: 555.Control_Voltage, C2.0
  N6: DELAYED_USB_POWER.GND, Q1.collector
  N7: Q1.base, R2.Pin_1
