# Fritzing sketch id3275_doorkeeper_RPI_1.PCBrev2_0 (saved by Fritzing 0.9.2b)
circuit board: 11.4214cm x 8.6467cm
breadboards: 1

parts:
  IC1 = ULN2803A [package=THT]
  U1 = RELAY-2 [package=relay-g5v]
  LED1 = RGB LED (com. cathode, rgb) [package="5 mm [THT]"]
  R1 = Resistor [tolerance=±5% resistance=220 package=THT]
  R2 = Resistor [tolerance=±5% resistance=220 package=THT]
  R3 = Resistor [tolerance=±5% resistance=220 package=THT]
  U2 = RELAY-2 [package=relay-g5v]
  U3 = RELAY-2 [package=relay-g5v]
  JP1 = Header 2 [package=jst-2-smd]
  JP2 = Header 2 [package=jst-2-smd]
  JP3 = Header 2 [package=jst-2-smd]
  J3 = Piezo Speaker
  U4 = RELAY-2 [package=relay-g5v]
  JP4 = Header 2 [package=jst-2-smd]
  R4 = Resistor [tolerance=±5% resistance=10k package=THT]
  LED2 = LED - 5mm [color="Red (633nm)" package="5 mm [THT]"]
  R5 = Resistor [tolerance=±5% resistance=220 package=THT]
  JP5 = Header 2 [package=jst-2-smd]
  JP6 = Header 2 [package=jst-2-smd]
  JP7 = Header 2 [package=jst-2-smd]
  J6 = shrouded pin header, 40 pins [form="♂ (shrouded male)"]

nets:
  N1: IC1.In_1, J6.pin28
  N2: IC1.In_2, J6.pin30
  N3: IC1.In_3, U3.10
  N4: IC1.In_4, R5.Pin_0, J6.pin27
  N5: IC1.In_5, JP5.1
  N6: IC1.In_6, JP6.1
  N7: IC1.In_7, JP7.1
  GND: IC1.0V, U1.9, LED1.common_cathode, U2.9, J3.pin1, U4.9, R4.Pin_0, LED2.cathode, J6.pin25
  N8: IC1.COM_-_Common, JP5.2, JP6.2, JP7.2
  N9: IC1.Out_7, J6.pin32
  N10: IC1.Out_6, J6.pin9
  N11: IC1.Out_5, J6.pin10
  N12: IC1.Out_4, U4.2
  N13: IC1.Out_3, R4.Pin_1, J6.pin31
  N14: IC1.Out_2, U2.2
  N15: IC1.Out_1, U1.2
  N16: U1.6, JP1.1
  N17: U1.10, JP1.2
  N18: LED1.red_anode, R1.Pin_1
  N19: LED1.green_anode, R3.Pin_1
  N20: LED1.blue_anode, R2.Pin_1
  N21: R2.Pin_0, J6.pin26
  N22: U2.6, JP2.1
  N23: U2.10, JP2.2
  N24: U3.2, JP3.1
  N25: U3.6, J3.pin2
  N26: U3.9, JP3.2
  N27: U4.6, JP4.1
  N28: U4.10, JP4.2
  N29: LED2.anode, R5.Pin_1

notes:
  Door keeper Raspberry PI
  Gache Bas (out)
  Gache Haut (out)
  Sonnette (IN)
  Avertisseur externe (out)
  Ext.Bell
  Bell(in)
  Door2
  Door1
  DoorKeeper V2
  Buzzer
  PullDown
  ULN2803A
  P1
  External command buttons
  Rev 2-201506290100
