# Fritzing sketch id3276_dual_motor_0 (saved by Fritzing 0.9.0b)
breadboards: 1

parts:
  IC2 = L293D [package=THT]
  Raspberry_Pi1 = Raspberry Pi B rev2
  M1 = DC Motor
  M2 = DC Motor
  VCC1 = 4 x AAA Battery Mount

nets:
  N1: IC2.Enable_1, Raspberry_Pi1.GPIO_17
  N2: IC2.In_1, Raspberry_Pi1.GPIO_27
  N3: IC2.Out_1_(_Controlled_by_Enable_1_), M2.pin_2
  N4: IC2.0V, Raspberry_Pi1.GND, VCC1.-
  N5: IC2.Out_2_(_Controlled_by_Enable_1_), M2.pin_1
  N6: IC2.In_2, Raspberry_Pi1.GPIO_22
  N7: IC2.+Vmotor, VCC1.+
  N8: IC2.Enable_2, Raspberry_Pi1.GPIO_2
  N9: IC2.In_3, Raspberry_Pi1.GPIO_3
  N10: IC2.Out_3_(_Controlled_by_Enable_2_), M1.pin_2
  N11: IC2.Out_4_(_Controlled_by_Enable_2_), M1.pin_1
  N12: IC2.In_4, Raspberry_Pi1.GPIO_4
  N13: IC2.+V, Raspberry_Pi1.5V
