# Fritzing sketch id3278_LED_01_0 (saved by Fritzing 0.9.3b)
breadboards: 1

parts:
  Raspberry_Pi_1 = Raspberry Pi 3 [part_number=RPI-3-V1.2]
  LED1 = smd LED [color="Red (633nm)" package="0603 [SMD]"]
  R1 = Resistor [tolerance=±5% resistance=330k package="1206 [SMD]"]

nets:
  N1: Raspberry_Pi_1.GND, R1.Pin_0
  N2: Raspberry_Pi_1.GPIO18, LED1.anode
  N3: LED1.cathode, R1.Pin_1
