# Fritzing sketch id3280_Pi_Intruder_0 (saved by Fritzing 0.9.2b)
breadboards: 1

parts:
  Raspberry_Pi1 = Raspberry Pi B+
  PIR1 = PIR_sensor
  LED1 = smd LED [color="Red (633nm)" package="0603 [SMD]"]
  R1 = Resistor [tolerance=±5% resistance=220 package="0603 [SMD]"]

nets:
  N1: Raspberry_Pi1.GPIO17, LED1.anode
  N2: Raspberry_Pi1.GND, PIR1.connector3, R1.Pin_1
  N3: Raspberry_Pi1.GPIO18, PIR1.connector2
  N4: Raspberry_Pi1.5V, PIR1.connector1
  N5: LED1.cathode, R1.Pin_0

notes:
  Place Pi Camera in Camera Slot
