# Fritzing sketch id3282_Raspberry_Pi_Nightlight_0 (saved by Fritzing 0.9.3b)
breadboards: 1

parts:
  Raspberry_Pi_1 = Raspberry Pi 3 [part_number=RPI-3-V1.2]
  C2 = Electrolytic Capacitor [capacitance=1µF package="100 mil [THT, electrolytic]"]
  R1 = Photocell (LDR) [package=THT]
  LED1 = LED - 5mm [color="Red (633nm)" package="5 mm [THT]"]

nets:
  N1: Raspberry_Pi_1.3v3, R1.pin_0
  N2: Raspberry_Pi_1.GIPO4, C2.-, R1.pin_1
  N3: Raspberry_Pi_1.GND, C2.+, LED1.cathode
  N4: Raspberry_Pi_1.GIPO14, LED1.anode
