# Fritzing sketch id3283_nokia_graph_0 (saved by Fritzing 0.9.3b)
breadboards: 1

parts:
  Raspberry_Pi1 = Raspberry Pi B+
  Nokia_5110_LCD_Module1 = Nokia5110LCDModule

nets:
  N1: Raspberry_Pi1.3v3, Nokia_5110_LCD_Module1.connector5, Nokia_5110_LCD_Module1.connector6
  N2: Raspberry_Pi1.GPIO10, Nokia_5110_LCD_Module1.connector3
  N3: Raspberry_Pi1.GPIO11, Nokia_5110_LCD_Module1.connector4
  N4: Raspberry_Pi1.GPIO8, Nokia_5110_LCD_Module1.connector1
  N5: Raspberry_Pi1.GPIO24, Nokia_5110_LCD_Module1.connector0
  N6: Raspberry_Pi1.GPIO23, Nokia_5110_LCD_Module1.connector2
  N7: Raspberry_Pi1.GND, Nokia_5110_LCD_Module1.connector7
