# Fritzing sketch id3284_osgi_iot1a_0 (saved by Fritzing 0.9.2b)
circuit board: 6.45747cm x 5.63768cm
breadboards: 1

parts:
  J1 = prefix0000 [form="♀ (female)"]
  IC2 = ULN2003A [package="DIP16 [THT]"]
  IC1 = H-Bridge [package=THT]
  J2 = prefix0000 [form="♂ (male)"]
  J3 = prefix0000 [form="♂ (male)"]
  TRS1 = Audio Jack (TRS) 3.5mm [package="4Ucon 08780 [THT]"]
  J4 = male pin header, 4 pins [form="♂ (male)"]
  J5 = male pin header, 4 pins [form="♂ (male)"]
  J6 = male pin header, 4 pins [form="♂ (male)"]
  J7 = male pin header, 4 pins [form="♂ (male)"]
  J8 = male pin header, 4 pins [form="♂ (male)"]
  R2 = Resistor [tolerance=±5% resistance=220 package=THT]
  R3 = Resistor [tolerance=±5% resistance=220 package=THT]
  R4 = Resistor [tolerance=±5% resistance=220 package=THT]
  R5 = Resistor [tolerance=±5% resistance=220 package=THT]
  R6 = Resistor [tolerance=±5% resistance=220 package=THT]
  R7 = Resistor [tolerance=±5% resistance=220 package=THT]
  R1 = Resistor [tolerance=±5% resistance=150 package=THT]
  D1 = Rectifier Diode [part_number=1N4001 package="300 mil [THT]"]

nets:
  N1: J1.connector0, J1.connector8, J2.connector0, J3.connector0
  N2: J1.connector1, IC1.1A
  N3: J1.connector2, IC1.2A
  N4: J1.connector3, IC1.3A
  GND1: J1.connector4, J1.connector12, J1.connector19, IC2.0V, IC1.GND1, IC1.GND2, IC1.GND3, IC1.GND4, J2.connector2, J3.connector2, J4.pin1
  N5: J1.connector5, IC2.In_1
  N6: J1.connector6, IC1.4A
  N7: J1.connector7, IC2.In_7
  N8: J1.connector9, J2.connector5, J3.connector5
  N9: J1.connector10, J2.connector4, J3.connector4
  N10: J1.connector11, J2.connector6, J3.connector6
  N11: J1.connector14, IC2.In_6
  N12: J1.connector15, IC2.In_5
  N13: J1.connector16, IC2.In_4
  N14: J1.connector17, IC2.In_3
  N15: J1.connector18, IC2.In_2
  N16: J1.connector27, J3.connector7
  N17: J1.connector28, J2.connector7
  N18: J1.connector29, J2.connector1, J3.connector1
  N19: J1.connector38, J1.connector39, IC2.COM_-_Common, IC1.1_2EN, IC1.3_4EN, IC1.VCC1, TRS1.Tip, J7.pin1, J8.pin4
  N20: IC2.Out_7, R7.Pin_0
  N21: IC2.Out_6, R6.Pin_0
  N22: IC2.Out_5, R5.Pin_0
  N23: IC2.Out_4, R4.Pin_0
  N24: IC2.Out_3, R3.Pin_0
  N25: IC2.Out_2, R2.Pin_0
  N26: IC2.Out_1, R1.Pin_0
  N27: IC1.1Y, J5.pin2
  N28: IC1.2Y, J5.pin3
  N29: IC1.VCC2, D1.cathode
  N30: IC1.3Y, J6.pin2
  N31: IC1.4Y, J6.pin3
  N32: J2.connector3, J3.connector3
  N33: TRS1.Sleeve, R1.Pin_1
  N34: J4.pin4, D1.anode
  N35: J7.pin2, R7.Pin_1
  N36: J7.pin3, R6.Pin_1
  N37: J7.pin4, R5.Pin_1
  N38: J8.pin1, R4.Pin_1
  N39: J8.pin2, R3.Pin_1
  N40: J8.pin3, R2.Pin_1

notes:
  Dual Segment
  Controller
  IoT Demo 2015
  9V
  3V
  RFIDs
  Motors
  RST
  GND
  IRQ
  MISO
  MOSI
  SCLK
  SDA
  TM
  Designed by
  Sep 2015
  Rev 1.0
  LEDs
