# Fritzing sketch id3285_RPIDoorSensor_0 (saved by Fritzing 0.9.2b)

parts:
  Raspberry_Pi1 = Raspberry Pi 2
  Part1 = Triple Axis Accelerometer Breakout - ADXL345

nets:
  3V3: Raspberry_Pi1.3v3, Part1.VCC
  N1: Raspberry_Pi1.GPIO2, Part1.SDA
  N2: Raspberry_Pi1.GPIO3, Part1.SCL
  GND: Raspberry_Pi1.GND, Part1.GND
