# Fritzing sketch id3287_CoffeeTablePiPCB_0 (saved by Fritzing 0.8.8b)
circuit board: 8.46667cm x 5.64444cm
breadboards: 2

parts:
  R1 = Resistor [tolerance=±5% resistance=10k package=THT]
  1 = Screw terminal - 2 pins [package=THT]
  2 = Screw terminal - 2 pins [package=THT]
  3 = Screw terminal - 2 pins [package=THT]
  4 = Screw terminal - 2 pins [package=THT]
  8 = Screw terminal - 2 pins [package=THT]
  7 = Screw terminal - 2 pins [package=THT]
  6 = Screw terminal - 2 pins [package=THT]
  5 = Screw terminal - 2 pins [package=THT]
  R2 = Resistor [tolerance=±5% resistance=10k package=THT]
  R3 = Resistor [tolerance=±5% resistance=10k package=THT]
  R4 = Resistor [tolerance=±5% resistance=10k package=THT]
  R5 = Resistor [tolerance=±5% resistance=10k package=THT]
  R6 = Resistor [tolerance=±5% resistance=10k package=THT]
  R7 = Resistor [tolerance=±5% resistance=10k package=THT]
  R8 = Resistor [tolerance=±5% resistance=10k package=THT]
  R9 = Resistor [tolerance=±5% resistance=10k package=THT]
  12V = Power plug
  Q1 = Basic FET N-Channel [package="TO220 [THT]"]
  Q2 = Basic FET N-Channel [package="TO220 [THT]"]
  Q3 = Basic FET N-Channel [package="TO220 [THT]"]
  Q4 = Basic FET N-Channel [package="TO220 [THT]"]
  R13 = Resistor [tolerance=±5% resistance=10k package=THT]
  R14 = Resistor [tolerance=±5% resistance=10k package=THT]
  R15 = Resistor [tolerance=±5% resistance=10k package=THT]
  R16 = Resistor [tolerance=±5% resistance=10k package=THT]
  9 = Screw terminal - 2 pins [package=THT]
  10 = Screw terminal - 2 pins [package=THT]
  11 = Screw terminal - 2 pins [package=THT]
  12 = Screw terminal - 2 pins [package=THT]
  Raspberry_Pi_B_rev1 = Raspberry Pi B rev2
  D1 = Rectifier Diode [part_number=1N4001 package="300 mil [THT]"]

nets:
  N1: R1.Pin_0, 1.pin2, Raspberry_Pi_B_rev1.GPIO_7
  GND: R1.Pin_1, R2.Pin_1, R3.Pin_1, R4.Pin_1, R5.Pin_1, R6.Pin_1, R7.Pin_1, R8.Pin_1, 12V.GND, Q1.source, Q2.source, Q3.source, Q4.source, R13.Pin_0, R14.Pin_0, R15.Pin_0, R16.Pin_0, Raspberry_Pi_B_rev1.GND
  N2: 1.pin1, 2.pin1, 3.pin1, 4.pin1, 8.pin1, 7.pin1, 6.pin1, 5.pin1, R9.Pin_1
  N3: 2.pin2, R2.Pin_0, Raspberry_Pi_B_rev1.GPIO_8
  N4: 3.pin2, R3.Pin_0, Raspberry_Pi_B_rev1.GPIO_25
  N5: 4.pin2, R4.Pin_0, Raspberry_Pi_B_rev1.GPIO_24
  N6: 8.pin2, R5.Pin_0, Raspberry_Pi_B_rev1.GPIO_14
  N7: 7.pin2, R6.Pin_0, Raspberry_Pi_B_rev1.GPIO_15
  N8: 6.pin2, R7.Pin_0, Raspberry_Pi_B_rev1.GPIO_18
  N9: 5.pin2, R8.Pin_0, Raspberry_Pi_B_rev1.GPIO_23
  N10: R9.Pin_0, Raspberry_Pi_B_rev1.5V
  N11: 12V.VCC, D1.anode
  N12: Q1.gate, R13.Pin_1, Raspberry_Pi_B_rev1.GPIO_22
  N13: Q1.drain, 9.pin1
  N14: Q2.gate, R14.Pin_1, Raspberry_Pi_B_rev1.GPIO_10
  N15: Q2.drain, 10.pin1
  N16: Q3.gate, R15.Pin_1, Raspberry_Pi_B_rev1.GPIO_9
  N17: Q3.drain, 11.pin1
  N18: Q4.gate, R16.Pin_1, Raspberry_Pi_B_rev1.GPIO_11
  N19: Q4.drain, 12.pin1
  N20: 9.pin2, 10.pin2, 11.pin2, 12.pin2, D1.cathode
