# Fritzing sketch id3289_Simple_LED_on_off_with_Raspberry_Pi_0 (saved by Fritzing 0.7.9b)
breadboards: 1

parts:
  Raspberry_Pi1 = Raspberry_Pi__Model_B
  part = Pushbutton [package="[THT]"]  # not connected
  part_2 = Pushbutton [package="[THT]"]  # not connected
  part_3 = Trimmer Potentiometer [maximum_resistance=10kΩ package=THT]  # not connected
  part_4 = Pushbutton [package="[THT]"]  # not connected
  LED1 = LED - 3mm [color="Red (633nm)" package="3 mm [THT]"]
  R1 = Resistor [tolerance=±5% resistance=330 package=THT]

nets:
  N1: Raspberry_Pi1.connector6, R1.Pin_0
  N2: Raspberry_Pi1.connector11, LED1.anode
  N3: LED1.cathode, R1.Pin_1

notes:
  Simple Raspberry Pi project to control an LED on/off from GPIO pin 17.
  Red wire from GPIO#17 to live rail.
  Black wire from GPIO Ground to ground rail.
  Then, 330o resistor from ground rail to LED negative terminal.
  Then, red wire from LED positive terminal to live rail.
