# Fritzing sketch id328_22a___AND_Gate_Virtual_Logic_Activity_0 (saved by Fritzing 0.9.3b)
breadboards: 1

parts:
  IC1 = IC, DIP package, 14 pins [chip_label="IC 7404" part_number=7404]
  LED1 = LED - 5mm [color="Red (633nm)" package="5 mm [THT]"]
  VCC1 = 4 x AAA Battery Mount
  S1 = Pushbutton [package=THT]  # not connected
  S2 = Pushbutton [package=THT]
  S3 = Pushbutton [package=THT]
  R1 = Resistor [tolerance=±5% resistance=330 package=THT]

nets:
  N1: IC1.pin7, LED1.cathode, VCC1.-
  N2: IC1.pin8, R1.Pin_0
  N3: IC1.pin9, S3.leg1
  N4: IC1.pin10, IC1.pin11
  N5: IC1.pin12, S2.leg1
  N6: IC1.pin14, VCC1.+, S2.leg0, S3.leg0
  N7: LED1.anode, R1.Pin_1

notes:
  A
  B
  C
