# Fritzing sketch id3290_Raspberry_Pi_Sound_Machine_0 (saved by Fritzing 0.9.3b)
breadboards: 1

parts:
  Raspberry_Pi_1 = Raspberry Pi 3 [part_number=RPI-3-V1.2]
  S1 = Pushbutton [package="[THT]"]
  R1 = Resistor [tolerance=±5% resistance=10k package=THT]
  J1 = Piezo Speaker

nets:
  N1: Raspberry_Pi_1.3v3, S1.Pin_3, S1.Pin_4
  N2: Raspberry_Pi_1.GIPO15, J1.pin2
  N3: Raspberry_Pi_1.GIPO14, S1.Pin_1, S1.Pin_2, R1.Pin_0
  N4: Raspberry_Pi_1.GND, R1.Pin_1, J1.pin1
