# Fritzing sketch id3291_TempSensors_V2_0 (saved by Fritzing 0.8.3b)
circuit board: 2.58234cm x 7.1967cm
breadboards: 1

parts:
  Sensor_1 = screw terminal, 3 pins
  Sensor_2 = screw terminal, 3 pins
  Sensor_3 = screw terminal, 3 pins
  Sensor_4 = screw terminal, 3 pins
  Sensor_5 = screw terminal, 3 pins
  4_7k_Ohm = Resistor [tolerance=±5% resistance=220 package=THT]
  Pi_Connection = shrouded pin header, 26 pins [form="♂ (shrouded male)"]

nets:
  N1: Sensor_1.pin1, Sensor_2.pin1, Sensor_3.pin1, Sensor_4.pin1, Sensor_5.pin1, Pi_Connection.pin24
  N2: Sensor_1.pin2, Sensor_2.pin2, Sensor_3.pin2, Sensor_4.pin2, Sensor_5.pin2, 4_7k_Ohm.Pin_0, Pi_Connection.pin4
  N3: Sensor_1.pin3, Sensor_2.pin3, Sensor_3.pin3, Sensor_4.pin3, Sensor_5.pin3, 4_7k_Ohm.Pin_1, Pi_Connection.pin1

notes:
  Temp Sensor Connector
