# Fritzing sketch id3292_Motion_sensor (saved by Fritzing 0.6.2b)
breadboards: 1

parts:
  J3 = Infrared Proximity Sensor
  LED1 = Red LED - 5mm [package="5 mm [THT]"]
  Power_plug1 = Power plug
  R2 = Resistor [tolerance=±5% resistance=470 package="1206 [SMD]"]
  R3 = Resistor [tolerance=±5% resistance=470 package="0805 [SMD]"]

nets:
  N1: J3.Vout, R3.Pin_0
  GND: J3.GND, LED1.cathode, Power_plug1.GND
  VCC: J3.Vcc, Power_plug1.VCC
  N2: LED1.anode, R2.Pin_1
  N3: R2.Pin_0, R3.Pin_1
