# Fritzing sketch id3292_TempSensors_0 (saved by Fritzing 0.8.3b)
circuit board: 2.58231cm x 7.47891cm
breadboards: 1

parts:
  Sensor_1 = Header 3 [package=screwterminal-3.5mm-3_lock.007s]
  Sensor_2 = Header 3 [package=screwterminal-3.5mm-3_lock.007s]
  Sensor_3 = Header 3 [package=screwterminal-3.5mm-3_lock.007s]
  Sensor_4 = Header 3 [package=screwterminal-3.5mm-3_lock.007s]
  Sensor_5 = Header 3 [package=screwterminal-3.5mm-3_lock.007s]
  4_7k_Ohm = Resistor [tolerance=±5% resistance=4.7 package=THT]
  Pi_Connection = shrouded pin header, 26 pins [form="♂ (shrouded male)"]

nets:
  N1: Sensor_1.1, Sensor_2.1, Sensor_3.1, Sensor_4.1, Sensor_5.1, Pi_Connection.pin24
  N2: Sensor_1.2, Sensor_2.2, Sensor_3.2, Sensor_4.2, Sensor_5.2, 4_7k_Ohm.Pin_1, Pi_Connection.pin4
  N3: Sensor_1.3, Sensor_2.3, Sensor_3.3, Sensor_4.3, Sensor_5.3, 4_7k_Ohm.Pin_0, Pi_Connection.pin1
