# Fritzing sketch id3294_timetemp_0 (saved by Fritzing 0.7.7b)
breadboards: 1

parts:
  Pi1 = Pi_Cobbler
  RTC1 = DS1307_RTC_Breakout
  7SEG2 = 7_Segment_LED_I2C_Backpack__red
  Part1 = Digital Temperature Sensor Breakout - TMP102

nets:
  N1: Pi1.connector1, 7SEG2.connector1, Part1.V+
  N2: Pi1.connector2, RTC1.connector2
  N3: Pi1.connector3, RTC1.connector3, 7SEG2.connector3, Part1.SDA
  N4: Pi1.connector5, RTC1.connector4, 7SEG2.connector4, Part1.SCL
  N5: Pi1.connector6, RTC1.connector1, 7SEG2.connector2, Part1.GND
