# Fritzing sketch id3295_timetemp_0 (saved by Fritzing 0.7.7b)
breadboards: 1

parts:
  Pi1 = Pi_Cobbler
  RTC1 = DS1307_RTC_Breakout
  Part1 = Digital Temperature Sensor Breakout - TMP102
  7SEG2 = 7_Segment_LED_I2C_Backpack__red
  S1 = Pushbutton [package="[THT]"]
  R2 = Resistor [tolerance=±5% resistance=10k package=THT]

nets:
  N1: Pi1.connector1, Part1.V+, 7SEG2.connector1, R2.Pin_1
  N2: Pi1.connector2, RTC1.connector2
  N3: Pi1.connector3, RTC1.connector3, Part1.SDA, 7SEG2.connector3
  N4: Pi1.connector5, RTC1.connector4, Part1.SCL, 7SEG2.connector4
  N5: Pi1.connector6, RTC1.connector1, Part1.GND, 7SEG2.connector2, S1.Pin_1, S1.Pin_2
  N6: Pi1.connector16, S1.Pin_3, S1.Pin_4, R2.Pin_0
