# Fritzing sketch id3296_UPS_0 (saved by Fritzing 0.9.3b)

parts:
  S1 = SWITCH-MOMENTARY-2 [package=tactile-switch-1101ne]
  U1 = Unproven! [package=msop-10]
  Q1 = NPN-Transistor [package="SOT-23 [SMD]"]
  U2 = Battery Holders [package=lipo-1100mAh]
  Part1 = Arduino Mini (Rev5)
  U5 = Transformer 5v
  Raspberry_Pi_Zero1 = Raspberry Pi Zero
  R1 = Resistor [tolerance=±5% resistance=220 package=THT]

nets:
  N1: S1.1, U1.VBAT, Q1.1, U2.+
  N2: S1.2, Q1.2, U2.-
  N3: U1.VDD, U5.connector0, U5.connector1
  N4: Q1.0, R1.Pin_0
  N5: Part1.D0/TX, Raspberry_Pi_Zero1.GPIO15
  N6: Part1.D1/RX, Raspberry_Pi_Zero1.GPIO14
  N7: Part1.D8, R1.Pin_1
  GND: Part1.GND, U5.connector5, Raspberry_Pi_Zero1.GND
  5V: Part1.5V, U5.connector6, Raspberry_Pi_Zero1.5V
