# Fritzing sketch id3297_UselessBox_0 (saved by Fritzing 0.9.2b)
breadboards: 1

parts:
  Raspberry_Pi1 = Raspberry Pi 2
  JACK1 = 2.1mm_Barrel_Jack_with_Terminal_Block
  J1 = Basic Servo
  R1 = Resistor [tolerance=±5% resistance=1k package=THT]
  S1 = Toggle Switch [package=THT]

nets:
  N1: Raspberry_Pi1.GPIO4, S1.L1
  GND: Raspberry_Pi1.GND, JACK1.connector2, J1.gnd, S1.COM
  N2: Raspberry_Pi1.GPIO18, R1.Pin_0
  N3: JACK1.connector1, J1.vcc
  N4: J1.pulse, R1.Pin_1

notes:
  5V
