# Fritzing sketch id3299_Water_Sensor_Schematic_v2_enno_0 (saved by Fritzing 0.9.2b)
breadboards: 1

parts:
  RaspberryPi1 = Raspberry_Pi_Model_B
  J1 = Piezo Speaker
  C1 = Electrolytic Capacitor [capacitance=10µF voltage=20V package="100 mil [THT, electrolytic]"]
  S1 = Pushbutton [package=THT]

nets:
  N1: RaspberryPi1.connector6, RaspberryPi1.connector8, J1.pin1, C1.-
  N2: RaspberryPi1.connector11, RaspberryPi1.connector13, J1.pin2
  N3: RaspberryPi1.connector12, C1.+, S1.leg0

notes:
  replace the switch with the water sensor
