# Fritzing sketch id329_DIY_KIT_for_Android__Arduino_experiments_0 (saved by Fritzing 0.7.5b)
breadboards: 2

parts:
  Q8 = LED - 3mm [color="Red (633nm)" package="3 mm [THT]"]
  Q1 = LED - 3mm [color="Red (633nm)" package="3 mm [THT]"]
  R11 = Resistor [tolerance=±5% resistance=220 package=THT]
  R7 = Resistor [tolerance=±5% resistance=220 package=THT]
  Q2 = LED - 3mm [color="Red (633nm)" package="3 mm [THT]"]
  R3 = Resistor [tolerance=±5% resistance=220 package=THT]
  Q3 = LED - 3mm [color="Red (633nm)" package="3 mm [THT]"]
  Q5 = LED - 3mm [color="Red (633nm)" package="3 mm [THT]"]
  R12 = Resistor [tolerance=±5% resistance=220 package=THT]
  Q6 = LED - 3mm [color="Red (633nm)" package="3 mm [THT]"]
  R8 = Resistor [tolerance=±5% resistance=220 package=THT]
  R4 = Resistor [tolerance=±5% resistance=220 package=THT]
  Part1 = Bluetooth Mate Silver
  Q7 = LED - 3mm [color="Red (633nm)" package="3 mm [THT]"]
  QS' = LED - 3mm [color="Yellow (595nm)" package="3 mm [THT]"]
  R9 = Resistor [tolerance=±5% resistance=220 package=THT]
  R5 = Resistor [tolerance=±5% resistance=220 package=THT]
  QS = LED - 3mm [color="Orange (620nm)" package="3 mm [THT]"]
  Q4 = LED - 3mm [color="Red (633nm)" package="3 mm [THT]"]
  R10 = Resistor [tolerance=±5% resistance=220 package=THT]
  R6 = Resistor [tolerance=±5% resistance=220 package=THT]
  Arduino1 = Arduino
  R13 = Resistor [tolerance=±5% resistance=220 package=THT]
  LED1 = LED - 5mm [color="Red (633nm)" package="5 mm [THT]"]
  R14 = Photocell (LDR) [package=THT]
  R15 = Resistor [tolerance=±5% resistance=10k package=THT]
  T1 = LM35 Temperature Sensor [package="TO92 [THT]"]
  LED2 = RGB LED (com. cathode, rgb) [package="5 mm [THT]"]
  R16 = Resistor [tolerance=±5% resistance=220 package=THT]
  R17 = Resistor [tolerance=±5% resistance=220 package=THT]
  R18 = Resistor [tolerance=±5% resistance=220 package=THT]
  IC1 = IC, DIP package, 16 pins [chip_label=CD4094 spacing=300mil]

nets:
  GND: Q8.cathode, Q1.cathode, Q2.cathode, Q3.cathode, Q5.cathode, Q6.cathode, Part1.GND, Q7.cathode, QS'.cathode, QS.cathode, Q4.cathode, Arduino1.GND, LED1.cathode, R15.Pin_0, T1.GND, LED2.common_cathode, IC1.pin8
  N1: Q8.anode, R10.Pin_1
  N2: Q1.anode, R3.Pin_1
  N3: R11.Pin_0, QS.anode
  N4: R11.Pin_1, IC1.pin9
  N5: R7.Pin_0, IC1.pin14
  N6: R7.Pin_1, Q5.anode
  N7: Q2.anode, R4.Pin_1
  N8: R3.Pin_0, IC1.pin4
  N9: Q3.anode, R5.Pin_1
  N10: R12.Pin_0, QS'.anode
  N11: R12.Pin_1, IC1.pin10
  N12: Q6.anode, R8.Pin_1
  N13: R8.Pin_0, IC1.pin13
  N14: R4.Pin_0, IC1.pin5
  N15: Part1.RX_5V, Arduino1.D1TX
  N16: Part1.TX_5V, Arduino1.D0RX
  VCC: Part1.VCC, Arduino1.+5V, R14.pin_1, T1.+Vs, IC1.pin16
  N17: Q7.anode, R9.Pin_1
  N18: R9.Pin_0, IC1.pin12
  N19: R5.Pin_0, IC1.pin6
  N20: Q4.anode, R6.Pin_1
  N21: R10.Pin_0, IC1.pin11
  N22: R6.Pin_0, IC1.pin7
  N23: Arduino1.D11, R13.Pin_0
  N24: Arduino1.D10, IC1.pin3
  N25: Arduino1.D9, IC1.pin15
  N26: Arduino1.D8, IC1.pin2
  N27: Arduino1.D7, IC1.pin1
  N28: Arduino1.D6, R17.Pin_0
  N29: Arduino1.D5, R18.Pin_0
  N30: Arduino1.D3, R16.Pin_0
  N31: Arduino1.A0, T1.Vout
  N32: Arduino1.A1, R14.pin_0, R15.Pin_1
  N33: R13.Pin_1, LED1.anode
  N34: LED2.red_anode, R16.Pin_1
  N35: LED2.green_anode, R17.Pin_1
  N36: LED2.blue_anode, R18.Pin_1

notes:
  Common cathode RGB LED
