# Fritzing sketch id32_schema (saved by Fritzing 0.9.3b)
circuit board: 8.46667cm x 5.64444cm
breadboards: 1

parts:
  J1 = Piezo Speaker
  Part1 = Arduino Uno (Rev3)
  R1 = Resistor [tolerance=±5% resistance=220 package=THT]
  LED1 = LED - 5mm [color="Red (633nm)" package="5 mm [THT]"]
  LED2 = LED - 5mm [color="Red (633nm)" package="5 mm [THT]"]
  LED3 = LED - 5mm [color="Red (633nm)" package="5 mm [THT]"]
  LED4 = LED - 5mm [color="Red (633nm)" package="5 mm [THT]"]
  LED5 = LED - 5mm [color="Red (633nm)" package="5 mm [THT]"]
  LED6 = LED - 5mm [color="Red (633nm)" package="5 mm [THT]"]
  R4 = Resistor [tolerance=±5% resistance=220 package=THT]
  S1 = Round Pushbutton
  S2 = Round Pushbutton

nets:
  N1: J1.pin1, Part1.GND, R1.Pin_1, R4.Pin_1
  N2: J1.pin2, Part1.D13/SCK
  N3: Part1.A0, Part1.D12/MISO, LED4.cathode, LED5.cathode, LED6.cathode, S2.leg1
  N4: Part1.A1, Part1.D8, LED1.cathode, LED2.cathode, LED3.cathode, S1.leg1
  N5: Part1.5V, S1.leg0, S2.leg0
  N6: R1.Pin_0, LED4.anode, LED5.anode, LED6.anode
  N7: LED1.anode, LED2.anode, LED3.anode, R4.Pin_0

notes:
  Cable rojo es corriente directa de 5 voltios
  Cable negro negativo (tierra)
  Cables verdes entradas A0 y A1 (coneccion con botones y leds)
  Cables purpuras salidas mantiene encendido leds
  Cable rosa disparador para bipper (bocinita)
  Cables naranjass corriente para leds
  Los 3 leds pueden llevar una resistencia, aunque es recomendable tener una resistencia para cada foco
  Cables grises, son los que mandan el pulso del boton
  Cables amarillos, corriente leds
