# Fritzing sketch id3300_leds_0 (saved by Fritzing 0.9.1b)
breadboards: 1

parts:
  U1 = SN74LS21N [package="DIP14 [THT]"]
  VCC1 = 4 x AAA Battery Mount
  Raspberry_Pi1 = Raspberry Pi B+
  LPD8806_RGB_LED_Strip1 = LPD8806_RGB_LED_Strip

nets:
  GND: U1.1A, U1.1C, U1.GND, VCC1.-, Raspberry_Pi1.GND, LPD8806_RGB_LED_Strip1.connector4
  N1: U1.1B, Raspberry_Pi1.GPIO9, Raspberry_Pi1.GPIO11
  N2: U1.NC#2, LPD8806_RGB_LED_Strip1.connector5
  N3: U1.1D, Raspberry_Pi1.GPIO8
  N4: U1.1Y, LPD8806_RGB_LED_Strip1.connector6
  N5: U1.VCC, VCC1.+, LPD8806_RGB_LED_Strip1.connector7
