# Fritzing sketch id3301_Raspberry_PI_DS18B20_0 (saved by Fritzing 0.9.3b)

parts:
  DS1 = DS18B20 1-Wire Temperature Sensor [part_number=DS18B20]
  Raspberry_Pi1 = Raspberry Pi 2
  R1 = Resistor [tolerance=±5% resistance=4.7k package=THT]

nets:
  GND: DS1.GND, Raspberry_Pi1.GND
  N1: DS1.DQ, Raspberry_Pi1.GPIO4, R1.Pin_0
  3V3: DS1.VDD, Raspberry_Pi1.3v3, Raspberry_Pi1.3V3, R1.Pin_1
