# Fritzing sketch id3303_Motor_PI_0 (saved by Fritzing 0.9.3b)
breadboards: 1

parts:
  MCU1 = Raspberry Pi Zero
  IC1 = L293D [package=THT]
  M1 = DC Motor
  VCC1 = 4 x AAA Battery Mount

nets:
  N1: MCU1.pin_2, MCU1.pin_4, IC1.+V
  N2: MCU1.pin_6, MCU1.pin_39, IC1.0V, VCC1.-
  N3: MCU1.pin_11, IC1.In_1
  N4: MCU1.pin_13, IC1.In_2
  N5: MCU1.pin_15, IC1.Enable_1
  N6: IC1.Out_1_(_Controlled_by_Enable_1_), M1.pin_2
  N7: IC1.Out_2_(_Controlled_by_Enable_1_), M1.pin_1
  N8: IC1.+Vmotor, VCC1.+
