# Fritzing sketch id3304_Simple_Motor_Control_2_PWMs_0 (saved by Fritzing 0.9.2b)
breadboards: 1

parts:
  U1 = TA7291P
  VCC1 = 4 x AAA Battery Mount
  M1 = DC Motor
  Raspberry_Pi_Zero1 = Raspberry Pi Zero

nets:
  N1: U1.connector1, VCC1.-, Raspberry_Pi_Zero1.GND
  N2: U1.connector2, M1.pin_2
  N3: U1.connector4, U1.connector8, VCC1.+
  N4: U1.connector5, Raspberry_Pi_Zero1.GIPO18
  N5: U1.connector6, Raspberry_Pi_Zero1.GIPO19
  N6: U1.connector7, Raspberry_Pi_Zero1.5V
  N7: U1.connector10, M1.pin_1
