# Fritzing sketch id3307_Raspberry__nokia_5110_temperature_0 (saved by Fritzing 0.9.0b)
breadboards: 1

parts:
  Raspberry_Pi1 = Raspberry Pi B rev2
  T1 = DS18B20_Temperature_Sensor [part_number=DS18B20]
  R1 = Resistor [tolerance=±5% resistance=4.7k package="0603 [SMD]"]

nets:
  N1: Raspberry_Pi1.3V3, T1.connector2, R1.Pin_0
  N2: Raspberry_Pi1.GPIO_3, Raspberry_Pi1.GPIO_4, T1.connector1, R1.Pin_1
  N3: Raspberry_Pi1.GPIO_27, Raspberry_Pi1.GPIO_22
  N4: Raspberry_Pi1.GND, T1.connector0

notes:
  R1 = 4,7 K
  DS18B20
  Nokia 5510
