# Fritzing sketch id3308_Raspberry_DS18B20_temperature_0 (saved by Fritzing 0.9.0b)
breadboards: 1

parts:
  Raspberry_Pi_rev1 = Raspberry Pi rev2
  R1 = Resistor [tolerance=±5% resistance=4.7k package=THT]
  T1 = DS18B20_Temperature_Sensor [part_number=DS18B20]

nets:
  N1: Raspberry_Pi_rev1.3V3, R1.Pin_0, T1.connector2
  N2: Raspberry_Pi_rev1.GND, T1.connector0
  N3: Raspberry_Pi_rev1.GPIO_23, R1.Pin_1, T1.connector1

notes:
  R1 = 4.7kΩ
