# Fritzing sketch id3310_NPE_Shield_0 (saved by Fritzing 0.9.0b)
breadboards: 1

parts:
  LED1 = LED - 5mm [color="Red (633nm)" package="5 mm [THT]"]
  LED2 = LED - 5mm [color="Red (633nm)" package="5 mm [THT]"]
  LED3 = LED - 5mm [color="Red (633nm)" package="5 mm [THT]"]
  Q1 = NPN-Transistor [package="TO92 [THT]"]
  Q2 = NPN-Transistor [package="TO92 [THT]"]
  Q3 = NPN-Transistor [package="TO92 [THT]"]
  U1 = TLP621 [package=THT]
  U2 = TLP621 [package=THT]
  U3 = TLP621 [package=THT]
  R2 = Resistor [tolerance=±5% resistance=10k package="0603 [SMD]"]
  R3 = Resistor [tolerance=±5% resistance=10k package="0603 [SMD]"]
  R4 = Resistor [tolerance=±5% resistance=10k package="0603 [SMD]"]
  R5 = Resistor [tolerance=±5% resistance=47 package="0603 [SMD]"]
  R6 = Resistor [tolerance=±5% resistance=47 package="0603 [SMD]"]
  R7 = Resistor [tolerance=±5% resistance=47 package="0603 [SMD]"]
  Raspberry_Pi_B_rev1 = Raspberry Pi B rev1
  R8 = Resistor [tolerance=±5% resistance=120 package="0603 [SMD]"]
  R11 = Resistor [tolerance=±5% resistance=120 package="0603 [SMD]"]
  R12 = Resistor [tolerance=±5% resistance=120 package="0603 [SMD]"]

nets:
  N1: LED1.cathode, R12.Pin_0
  N2: LED1.anode, LED2.anode, LED3.anode, Q1.E, Q2.E, Q3.E, R5.Pin_1, R6.Pin_1, R7.Pin_1, Raspberry_Pi_B_rev1.GND
  N3: LED2.cathode, R8.Pin_0
  N4: LED3.cathode, R11.Pin_0
  N5: Q1.B, R3.Pin_1
  N6: Q1.C, R8.Pin_1
  N7: Q2.B, R2.Pin_1
  N8: Q2.C, R11.Pin_1
  N9: Q3.B, R4.Pin_1
  N10: Q3.C, R12.Pin_1
  N11: U1.Pin_1, Raspberry_Pi_B_rev1.GPIO_4
  N12: U1.Pin_2, R3.Pin_0
  N13: U1.Pin_4, R5.Pin_0
  N14: U1.Pin_3, U2.Pin_3, U3.Pin_3, Raspberry_Pi_B_rev1.5V
  N15: U2.Pin_1, Raspberry_Pi_B_rev1.GPIO_17
  N16: U2.Pin_2, R2.Pin_0
  N17: U2.Pin_4, R6.Pin_0
  N18: U3.Pin_1, Raspberry_Pi_B_rev1.GPIO_22
  N19: U3.Pin_2, R4.Pin_0
  N20: U3.Pin_4, R7.Pin_0
