# Fritzing sketch id3311_NPE_Shield_1_0 (saved by Fritzing 0.9.0b)
breadboards: 2

parts:
  Q1 = NPN-Transistor [package="TO92 [THT]"]
  Q2 = NPN-Transistor [package="TO92 [THT]"]
  Q3 = NPN-Transistor [package="TO92 [THT]"]
  U1 = TLP621 [package=THT]
  U2 = TLP621 [package=THT]
  U3 = TLP621 [package=THT]
  R2 = Resistor [tolerance=±5% resistance=10k package="0603 [SMD]"]
  R3 = Resistor [tolerance=±5% resistance=10k package="0603 [SMD]"]
  R4 = Resistor [tolerance=±5% resistance=10k package="0603 [SMD]"]
  R5 = Resistor [tolerance=±5% resistance=47 package="0603 [SMD]"]
  R6 = Resistor [tolerance=±5% resistance=47 package="0603 [SMD]"]
  R7 = Resistor [tolerance=±5% resistance=47 package="0603 [SMD]"]
  Raspberry_Pi_B_rev1 = Raspberry Pi B rev1
  R8 = Resistor [tolerance=±5% resistance=120 package="0603 [SMD]"]
  R11 = Resistor [tolerance=±5% resistance=120 package="0603 [SMD]"]
  R12 = Resistor [tolerance=±5% resistance=120 package="0603 [SMD]"]
  U4 = MC14021
  J1 = Piezo Speaker
  BUTTON1 = Waterproof_Momentary_Pushbutton__red
  BUTTON2 = Waterproof_Pushbutton__green
  BUTTON3 = Waterproof_Pushbutton__blue
  R13 = Resistor [package="2512 [SMD]"]
  R14 = Resistor [package="2512 [SMD]"]
  R15 = Resistor [package="2512 [SMD]"]
  S1 = Round Pushbutton
  R16 = Resistor [package="2512 [SMD]"]
  Part2 = Arduino Uno (Rev3) - ICSP

nets:
  GND: Q1.E, Q2.E, Q3.E, R5.Pin_1, R6.Pin_1, R7.Pin_1, Raspberry_Pi_B_rev1.GND, U4.connector0, U4.connector1, U4.connector3, U4.connector5, U4.connector6, U4.connector7, J1.pin1, BUTTON1.connector4, BUTTON2.connector4, BUTTON3.connector4, R16.Pin_0, Part2.GND
  N1: Q1.B, R3.Pin_1
  N2: Q1.C, R8.Pin_1
  N3: Q2.B, R2.Pin_1
  N4: Q2.C, R11.Pin_1
  N5: Q3.B, R4.Pin_1
  N6: Q3.C, R12.Pin_1
  N7: U1.Pin_1, Raspberry_Pi_B_rev1.GPIO_4
  N8: U1.Pin_2, R3.Pin_0
  N9: U1.Pin_4, R5.Pin_0
  N10: U1.Pin_3, U2.Pin_3, U3.Pin_3, Raspberry_Pi_B_rev1.5V
  N11: U2.Pin_1, Raspberry_Pi_B_rev1.GPIO_17
  N12: U2.Pin_2, R2.Pin_0
  N13: U2.Pin_4, R6.Pin_0
  N14: U3.Pin_1, Raspberry_Pi_B_rev1.GPIO_22
  N15: U3.Pin_2, R4.Pin_0
  N16: U3.Pin_4, R7.Pin_0
  3V3: Raspberry_Pi_B_rev1.3V3, U4.connector15, BUTTON1.connector2, BUTTON2.connector2, BUTTON3.connector2, S1.leg0, Part2.5V
  N17: Raspberry_Pi_B_rev1.GPIO_18, U4.connector2
  N18: Raspberry_Pi_B_rev1.GPIO_24, U4.connector9
  N19: Raspberry_Pi_B_rev1.GPIO_10, Part2.ICSP_MOSI
  N20: Raspberry_Pi_B_rev1.GPIO_9, Part2.ICSP_MISO
  N21: Raspberry_Pi_B_rev1.GPIO_25, U4.connector8
  N22: Raspberry_Pi_B_rev1.GPIO_11, Part2.ICSP_SCK
  N23: Raspberry_Pi_B_rev1.GPIO_8, J1.pin2
  N24: Raspberry_Pi_B_rev1.GPIO_7, Part2.D9_PWM
  N25: R8.Pin_0, BUTTON3.connector5
  N26: R11.Pin_0, BUTTON2.connector5
  N27: R12.Pin_0, BUTTON1.connector5
  N28: U4.connector4, S1.leg1, R16.Pin_1
  N29: U4.connector11, R13.Pin_0, R14.Pin_0, R15.Pin_0
  N30: U4.connector12, BUTTON3.connector1, R13.Pin_1
  N31: U4.connector13, BUTTON2.connector1, R14.Pin_1
  N32: U4.connector14, BUTTON1.connector1, R15.Pin_1
