# Fritzing sketch id3312_RX_0 (saved by Fritzing 0.9.2b)
circuit board: 11.0804cm x 8.9568cm
stripboards: 1

parts:
  Raspberry_Pi_rev1 = Raspberry Pi rev2
  ATtiny1 = prefix0000
  RFM12b1 = RFM12b HopeRF Transceiver
  R1 = Resistor [tolerance=±5% resistance=10k package=THT]
  R2 = Resistor [tolerance=±5% resistance=10k package=THT]
  C1 = Ceramic Capacitor [capacitance=100nF package="100 mil [THT, multilayer]"]
  C2 = Ceramic Capacitor [capacitance=100nF package="100 mil [THT, multilayer]"]
  LED1 = LED - 5mm [color="Green (555nm)" package="5 mm [THT]"]

nets:
  N1: Raspberry_Pi_rev1.3V3, ATtiny1.connector0, ATtiny1.connector3, RFM12b1.9_VDD, R1.Pin_0, R1.Pin_1, R2.Pin_1, C1.0, C2.0
  N2: Raspberry_Pi_rev1.GND, ATtiny1.connector13, RFM12b1.7_GND, C1.1, C2.1, LED1.cathode
  N3: Raspberry_Pi_rev1.GPIO_14, ATtiny1.connector9
  N4: Raspberry_Pi_rev1.GPIO_15, ATtiny1.connector5
  N5: ATtiny1.connector1, ATtiny1.connector2, RFM12b1.14_nSEL, R2.Pin_0
  N6: ATtiny1.connector4, RFM12b1.6_nRES
  N7: ATtiny1.connector6, RFM12b1.1_SDO
  N8: ATtiny1.connector7, RFM12b1.12_SDI
  N9: ATtiny1.connector8, RFM12b1.13_SCK
  N10: ATtiny1.connector10, LED1.anode

notes:
  Rot = 3V3
  Schwarz = GND
  Orange = RX -> PA7 (pin6)
  Weiß = TX -> PA3 (pin10)
  Grau = nIRQ -> PB2 (pin5)
  Blau = SDO -> PA6 (pin7)
  Gelb = SDI -> PA5 (pin8)
  Grün = SCK -> PA4 (pin9)
  Braun-Weiß = nSEL -> PB1 (pin3)
  Rosa = LED -> PA2 (pin11)
  Violett = ANT
