# Fritzing sketch id3315_RPi2_RTC_0 (saved by Fritzing 0.9.2b)

parts:
  Raspberry_Pi2 = Raspberry Pi 2
  Part1 = Real Time Clock Module - DS1307 RTC Breakout Board

nets:
  N1: Raspberry_Pi2.GPIO2, Part1.SDA
  N2: Raspberry_Pi2.GPIO3, Part1.SCL
  GND: Raspberry_Pi2.GND, Part1.GND
  5V: Raspberry_Pi2.5V, Part1.5V
