# Fritzing sketch id3316_Untitled_Sketch_0 (saved by Fritzing 0.9.2b)

parts:
  Raspberry_Pi3 = Raspberry Pi 2
  J1 = RJ11 Jack [package=rj11-6]
  S1 = SWITCH-MOMENTARY-2 [package=reed_switch_plastic]
  J2 = RJ11 Jack [package=rj11-6]

nets:
  N1: Raspberry_Pi3.GPIO13, J1.6
  N2: Raspberry_Pi3.GND, J1.3
  N3: S1.1, J2.3
  N4: S1.2, J2.6
