# Fritzing sketch id3317_raspi3kad_0 (saved by Fritzing 0.9.3b)
breadboards: 1

parts:
  Raspberry_Pi_1 = Raspberry Pi 3 [part_number=RPI-3-V1.2]
  RHT1 = Humidity and Temperature Sensor RHT03
  RHT2 = Humidity and Temperature Sensor RHT03
  RHT3 = Humidity and Temperature Sensor RHT03
  RHT4 = Humidity and Temperature Sensor RHT03
  R2 = prefix0000
  R3 = prefix0000
  R4 = prefix0000
  R5 = prefix0000

nets:
  N1: Raspberry_Pi_1.GPIO4, RHT1.Vcc, R5.connector1
  N2: Raspberry_Pi_1.GPIO17, RHT2.Vcc, R2.connector1
  N3: Raspberry_Pi_1.GPIO5, RHT3.Vcc, R3.connector1
  N4: Raspberry_Pi_1.GPIO26, RHT4.Vcc, R4.connector1
  N5: Raspberry_Pi_1.GND, RHT1.GND_2, RHT2.GND_2, RHT3.GND_2, RHT4.GND_2
  N6: RHT1.Data-signal, R5.connector0
  N7: RHT2.Data-signal, R2.connector0
  N8: RHT3.Data-signal, R3.connector0
  N9: RHT4.Data-signal, R4.connector0
