# Fritzing sketch id3318_raspi_servo_0 (saved by Fritzing 0.9.3b)

parts:
  J1 = Basic Servo
  Raspberry_Pi1 = Raspberry Pi 2
  VCC1 = 4 x AAA Battery Mount
  J2 = Basic Servo

nets:
  GND: J1.gnd, Raspberry_Pi1.GND, VCC1.-, J2.gnd
  VCC: J1.vcc, VCC1.+, J2.vcc
  N1: J1.pulse, Raspberry_Pi1.GPIO17
  N2: Raspberry_Pi1.GPIO4, J2.pulse
