# Fritzing sketch id3319_RC_0 (saved by Fritzing 0.9.2b)
breadboards: 1

parts:
  C1 = Electrolytic Capacitor [capacitance=1µF package="100 mil [THT, electrolytic]"]
  R1 = Resistor [tolerance=±5% resistance=220 package=THT]
  VCC1 = Battery

nets:
  N1: C1.-, VCC1.-
  N2: C1.+, R1.Pin_1
  N3: R1.Pin_0, VCC1.+
