# Fritzing sketch id331_grbl_with_bluetooth_0 (saved by Fritzing 0.9.2b)
breadboards: 1

parts:
  부품1 = Arduino Uno (Rev3)
  C1 = Electrolytic Capacitor [capacitance=100µF package="100 mil [THT, electrolytic]"]
  MD09B2 = A4988 Stepper Motor Driver Carrier
  M1 = Stepper Motor - Bipolar
  MD09B3 = A4988 Stepper Motor Driver Carrier
  MD09B4 = A4988 Stepper Motor Driver Carrier
  Part1 = HC-06
  M2 = Stepper Motor - Bipolar
  M3 = Stepper Motor - Bipolar
  R1 = Resistor [tolerance=±5% resistance=1k package=THT]
  R2 = Resistor [tolerance=±5% resistance=2.2k package=THT]

nets:
  N1: 부품1.GND, C1.-, MD09B2.GROUND#141, MD09B3.GROUND#141, MD09B4.GROUND#141
  N2: 부품1.D0/RX, Part1.connector13
  N3: 부품1.D1/TX, R1.Pin_0, R2.Pin_1
  N4: 부품1.D2, MD09B4.STEP
  N5: 부품1.D3_PWM, MD09B3.STEP
  N6: 부품1.D4, MD09B2.STEP
  N7: 부품1.D5_PWM, MD09B4.DIR
  N8: 부품1.D6_PWM, MD09B3.DIR
  N9: 부품1.D7, MD09B2.DIR
  VDD: 부품1.5V, MD09B2.MS1, MD09B2.VDD, MD09B3.MS1, MD09B3.VDD, MD09B4.MS1, MD09B4.VDD, Part1.connector15
  N10: C1.+, MD09B2.VMOT, MD09B3.VMOT, MD09B4.VMOT
  N11: MD09B2.RESET, MD09B2.SLEEP
  N12: MD09B2.OUT_2B, M1.A
  N13: MD09B2.OUT_2A, M1.B
  N14: MD09B2.OUT_1A, M1.C
  N15: MD09B2.OUT_1B, M1.D
  N16: MD09B2.GROUND#147, MD09B3.GROUND#147, MD09B4.GROUND#147, R2.Pin_0
  N17: MD09B3.RESET, MD09B3.SLEEP
  N18: MD09B3.OUT_2B, M2.A
  N19: MD09B3.OUT_2A, M2.B
  N20: MD09B3.OUT_1A, M2.C
  N21: MD09B3.OUT_1B, M2.D
  N22: MD09B4.RESET, MD09B4.SLEEP
  N23: MD09B4.OUT_2B, M3.A
  N24: MD09B4.OUT_2A, M3.B
  N25: MD09B4.OUT_1A, M3.C
  N26: MD09B4.OUT_1B, M3.D
  N27: Part1.connector12, R1.Pin_1

notes:
  +5V
  +12V
  Gnd
