# Fritzing sketch id3320_AirCombatFrizzling_0 (saved by Fritzing 0.9.2b)
breadboards: 1
perfboards: 2

parts:
  Bauteil1 = Arduino Nano (Rev3.0)
  Transmitter_(desolder_receiver) = SRF05 Ultrasonic Rangefinder
  Piezzo_Buzzer = Buzzer 12mm [package=buzzer-12mm]
  Receiver_(desolder_transmitter_and_add_a_second_receiver) = SRF05 Ultrasonic Rangefinder

nets:
  N1: Bauteil1.GND, Transmitter_(desolder_receiver).connector11, Piezzo_Buzzer.1, Receiver_(desolder_transmitter_and_add_a_second_receiver).connector11
  N2: Bauteil1.D4, Receiver_(desolder_transmitter_and_add_a_second_receiver).connector9
  N3: Bauteil1.D5, Transmitter_(desolder_receiver).connector9
  N4: Bauteil1.D6, Receiver_(desolder_transmitter_and_add_a_second_receiver).connector10
  N5: Bauteil1.D8, Piezzo_Buzzer.2
  N6: Bauteil1.5V, Transmitter_(desolder_receiver).connector8, Receiver_(desolder_transmitter_and_add_a_second_receiver).connector8

notes:
  throttle
  gun trigger
