# Fritzing sketch id3321_AnalogInputOutput_0 (saved by Fritzing 0.9.3b)
circuit board: 6.88566cm x 5.36311cm
breadboards: 2

parts:
  R4 = Resistor [resistance=1k tolerance=±5% package=THT]
  LED2 = LED - 5mm [color="Red (633nm)" current=5mA package="5 mm [THT]"]
  Arduino2 = Arduino Uno (Rev3)
  C1 = Electrolytic Capacitor [capacitance=1µF package="100 mil [THT, electrolytic]"]

nets:
  N1: R4.Pin_0, LED2.cathode, LED2.anode, Arduino2.GND, C1.-, C1.+
  N2: R4.Pin_1, Arduino2.D3_PWM

notes:
  In this example, potentiometer values are read in through an 'Analog In' pin. The values are then used to control the modulation of an LED on a PWM pin. Related examples: http://arduino.cc/en/Tutorial/AnalogInput http://arduino.cc/en/Tutorial/Fading
