# Fritzing sketch id3322_rc_lights_0 (saved by Fritzing 0.7.1b)
perfboards: 1

parts:
  Arduino1 = Arduino
  R1 = Resistor [tolerance=±5% resistance=100 package=THT]
  R3 = Resistor [tolerance=±5% resistance=100 package=THT]
  R3_2 = Resistor [tolerance=±5% resistance=68 package=THT]
  R4 = Resistor [tolerance=±5% resistance=68 package=THT]
  LED2 = LED - 5mm [color="Red (633nm)" package="5 mm [THT]"]
  LED3 = LED - 5mm [color="White (8000K)" package="5 mm [THT]"]
  LED4 = LED - 5mm [color="White (8000K)" package="5 mm [THT]"]
  J3 = male pin header, 3 pins [form="♂ (male)"]
  J4 = male pin header, 3 pins [form="♂ (male)"]
  J1 = male pin header, 3 pins [form="♂ (male)"]
  J2 = male pin header, 3 pins [form="♂ (male)"]
  J5 = female pin header, 4 pins [form="♀ (female)"]
  J8 = male pin header, 4 pins [form="♂ (male)"]
  J6 = female pin header, 1 pin [form="♀ (female)"]  # not connected
  J7 = male pin header, 1 pin [form="♂ (male)"]
  LED1 = LED - 5mm [color="Red (633nm)" package="5 mm [THT]"]

nets:
  N1: Arduino1.GND, J3.pin3, J4.pin3
  N2: Arduino1.D9, R1.Pin_1
  N3: Arduino1.D8, R3.Pin_1
  N4: Arduino1.D7, R3_2.Pin_1
  N5: Arduino1.D6, R4.Pin_1
  N6: Arduino1.D5, J3.pin1, J4.pin1
  N7: Arduino1.D4, J1.pin1, J2.pin1
  N8: R1.Pin_0, J5.pin4
  N9: R3.Pin_0, J5.pin3
  N10: R3_2.Pin_0, J5.pin2
  N11: R4.Pin_0, J5.pin1
  N12: LED2.cathode, LED3.cathode, LED4.cathode, J7.pin1, LED1.cathode
  N13: LED3.anode, J8.pin2
  N14: LED4.anode, J8.pin1
  N15: J3.pin2, J4.pin2
  N16: J1.pin2, J2.pin2
  N17: J1.pin3, J2.pin3
  N18: J8.pin4, LED1.anode
