# Fritzing sketch id3323_SparkRdioButton_0 (saved by Fritzing 0.8.7b)
breadboards: 1

parts:
  U1 = SPARKCORE
  R1 = Resistor [tolerance=±5% resistance=220 package=THT]
  S1 = Pushbutton [package="[THT]"]

nets:
  N1: U1.connector53, R1.Pin_0
  N2: U1.connector61, U1.connector62, R1.Pin_1, S1.Pin_3, S1.Pin_4
  N3: S1.Pin_1, S1.Pin_2
