# Fritzing sketch id3324_whofirst_0 (saved by Fritzing 0.9.1b)
breadboards: 1

parts:
  LED1 = LED - 5mm [color="Green (555nm)" package="5 mm [THT]"]
  R1 = Resistor [tolerance=±5% resistance=220 package=THT]
  R2 = Resistor [tolerance=±5% resistance=220 package=THT]
  LED2 = LED - 5mm [color="Green (555nm)" package="5 mm [THT]"]
  S1 = Pushbutton [package="[THT]"]
  S2 = Pushbutton [package="[THT]"]
  U1 = ATTINY13 [package=dip]
  R3 = Resistor [tolerance=±5% resistance=220 package=THT]
  R4 = Resistor [tolerance=±5% resistance=220 package=THT]
  VCC1 = Battery

nets:
  N1: LED1.cathode, R1.Pin_1
  N2: LED1.anode, U1.PB2(SCK_ADC1)
  N3: R1.Pin_0, R2.Pin_0, S1.Pin_1, S1.Pin_2, S2.Pin_1, S2.Pin_2, U1.GND, VCC1.-
  N4: R2.Pin_1, LED2.cathode
  N5: LED2.anode, U1.PB3(ADC3)
  N6: S1.Pin_3, S1.Pin_4, U1.PB1(MISO), R4.Pin_0
  N7: S2.Pin_3, S2.Pin_4, U1.PB0(MOSI), R3.Pin_0
  N8: U1.VCC, R3.Pin_1, R4.Pin_1, VCC1.+
