# Fritzing sketch id3325_reactionGameStructure_0 (saved by Fritzing 0.9.1b)
breadboards: 1

parts:
  Raspberry_Pi1 = Raspberry Pi B rev2
  S1 = Pushbutton [package="[THT]"]
  S2 = Pushbutton [package="[THT]"]
  LED1 = LED - 5mm [color="Blue (525nm)" package="5 mm [THT]"]
  R1 = Resistor [tolerance=±5% resistance=220 package=THT]
  R2 = Resistor [tolerance=±5% resistance=220 package=THT]
  R3 = Resistor [tolerance=±5% resistance=220 package=THT]
  R4 = Resistor [tolerance=±5% resistance=220 package=THT]
  LED2 = LED - 5mm [color="Green (570nm)" package="5 mm [THT]"]
  LED3 = LED - 5mm [color="Orange (612nm)" package="5 mm [THT]"]
  LED4 = LED - 5mm [color="Red (633nm)" package="5 mm [THT]"]

nets:
  N1: Raspberry_Pi1.3V3, S1.Pin_1, S1.Pin_2, S2.Pin_1, S2.Pin_2
  N2: Raspberry_Pi1.GND, LED1.anode, LED2.anode, LED3.anode, LED4.anode
  N3: Raspberry_Pi1.GPIO_23, R2.Pin_0
  N4: Raspberry_Pi1.GPIO_17, S2.Pin_3, S2.Pin_4
  N5: Raspberry_Pi1.GPIO_18, R1.Pin_0
  N6: Raspberry_Pi1.GPIO_4, S1.Pin_3, S1.Pin_4, LED1.cathode
  N7: Raspberry_Pi1.GPIO_24, R3.Pin_0
  N8: Raspberry_Pi1.GPIO_25, R4.Pin_0
  N9: R2.Pin_1, LED2.cathode
  N10: R3.Pin_1, LED3.cathode
  N11: R4.Pin_1, LED4.cathode
