# Fritzing sketch id3327_Omron_rotary_encoder_Arduino_0 (saved by Fritzing 0.9.0b)
breadboards: 1

parts:
  Componente1 = Arduino Mega ADK (Rev3)
  R1 = Resistor [tolerance=±5% resistance=10k package="0603 [SMD]"]
  R2 = Resistor [tolerance=±5% resistance=10k package="0603 [SMD]"]

nets:
  N1: Componente1.5V, R1.Pin_0, R2.Pin_0
  N2: Componente1.D2_PWM, R1.Pin_1
  N3: Componente1.D3_PWM, R2.Pin_1

notes:
  Blue = Ground
  Brown = +5V
  Black = output pulse A
  White = output pulse B
  (Unused)
  Grey = shield
  Orange = output pulse Z
  This schema use Interrupt.
  For more info look:
  http://arduino.cc/en/Reference/attachInterrupt
