# Fritzing sketch id3328_readSPSTButtonArduino_0 (saved by Fritzing 0.9.2b)
breadboards: 1

parts:
  Part1 = Arduino Uno (Rev3)
  S1 = Square Pushbutton
  R1 = Resistor [tolerance=±5% resistance=1k package=THT]

nets:
  N1: Part1.GND, R1.Pin_0
  N2: Part1.D5_PWM, S1.leg1, R1.Pin_1
  N3: Part1.3V3, S1.leg0
