# Fritzing sketch id3329_Analog_Read_From_Potentiometer_0 (saved by Fritzing 0.9.3b)
circuit board: 12.084cm x 6.70914cm
breadboards: 1

parts:
  Mega2560 = Arduino Mega 2560 (Rev3)
  R1 = Trimmer Potentiometer [maximum_resistance=50kΩ package=THT]

nets:
  N1: Mega2560.A0, R1.wiper
  N2: Mega2560.5V, R1.leg1
  N3: Mega2560.GND, R1.leg2
