# Fritzing sketch id332_AndruinoR2_0 (saved by Fritzing 0.9.0b)
circuit board: 6.88566cm x 5.36311cm
breadboards: 1

parts:
  Motor2 = DC Motor
  Motor1 = DC Motor
  Batt2 = Battery
  Batt1 = Battery
  C1 = Electrolytic Capacitor [capacitance=47µF voltage=10V package="100 mil [THT, electrolytic]"]
  LDR3 = Photocell (LDR) [package=THT]
  LDR1 = Photocell (LDR) [package=THT]
  R1 = Resistor [tolerance=±10% resistance=10k package=THT]
  R2 = Resistor [tolerance=±10% resistance=10k package=THT]
  HC-SR04_2 = HC-SR04
  HC-SR04_1 = HC-SR04
  HC-SR04_3 = HC-SR04
  R3 = Resistor [tolerance=±10% resistance=10k package=THT]
  LDR2 = Photocell (LDR) [package=THT]
  L293D = L293D [package=THT]
  Arduino1 = Arduino Uno (Rev3)

nets:
  N1: Motor2.pin_1, L293D.Out_3_(_Controlled_by_Enable_2_)
  N2: Motor2.pin_2, L293D.Out_4_(_Controlled_by_Enable_2_)
  N3: Motor1.pin_1, L293D.Out_2_(_Controlled_by_Enable_1_)
  N4: Motor1.pin_2, L293D.Out_1_(_Controlled_by_Enable_1_)
  GND: Batt2.-, C1.-, LDR3.pin_0, LDR1.pin_0, HC-SR04_2.connector11, HC-SR04_1.connector11, HC-SR04_3.connector11, LDR2.pin_1, L293D.0V, Arduino1.GND
  N5: Batt2.+, Batt1.-
  N6: Batt1.+, L293D.+Vmotor
  5V: C1.+, R1.Pin_1, R2.Pin_0, HC-SR04_2.connector8, HC-SR04_1.connector8, HC-SR04_3.connector8, R3.Pin_1, L293D.Enable_1, L293D.Enable_2, L293D.+V, Arduino1.5V
  N7: LDR3.pin_1, R3.Pin_0, Arduino1.A2
  N8: LDR1.pin_1, R1.Pin_0, Arduino1.A0
  N9: R2.Pin_1, LDR2.pin_0, Arduino1.A1
  N10: HC-SR04_2.connector9, Arduino1.D8
  N11: HC-SR04_2.connector10, Arduino1.D7
  N12: HC-SR04_1.connector9, Arduino1.D11_PWM/MOSI
  N13: HC-SR04_1.connector10, Arduino1.D12/MISO
  N14: HC-SR04_3.connector9, Arduino1.D4
  N15: HC-SR04_3.connector10, Arduino1.D2
  N16: L293D.In_1, Arduino1.D5_PWM
  N17: L293D.In_2, Arduino1.D6_PWM
  N18: L293D.In_3, Arduino1.D10_PWM/SS
  N19: L293D.In_4, Arduino1.D9_PWM

notes:
  Arduino ROS
  andruino
