# Fritzing sketch id3330_8266_and_AM2303_0 (saved by Fritzing 0.9.3b)
breadboards: 1

parts:
  WeMos_D1_Mini1 = WeMos D1 Mini
  R1 = Resistor [tolerance=±5% resistance=220 package=THT]
  RHT1 = Humidity and Temperature Sensor RHT03

nets:
  3V3: WeMos_D1_Mini1.3V3, R1.Pin_0, RHT1.Vcc
  N1: WeMos_D1_Mini1.D2, R1.Pin_1, RHT1.Data-signal
  N2: WeMos_D1_Mini1.G, RHT1.GND_2
