# Fritzing sketch id3331_Redstone_Lamp_0 (saved by Fritzing 0.8.3b)
perfboards: 1

parts:
  Raspberry_Pi_rev1 = Raspberry Pi rev1
  Q1 = NPN-Transistor [package="TO92 [THT]"]
  Power_plug1 = Power plug
  R1 = Resistor [tolerance=±5% resistance=1k package=THT]
  LED1 = LEDs [package=led10mm]

nets:
  N1: Raspberry_Pi_rev1.GPIO_18, R1.Pin_0
  N2: Q1.E, Power_plug1.VCC
  N3: Q1.B, R1.Pin_1
  N4: Q1.C, LED1.A
  N5: Power_plug1.GND, LED1.C

notes:
  NPN transistor
  Shown here E-B-C
  1kΩ resistor
  This LED in place of a string of them.
  12V DC for LEDs
  Red is +
