# Fritzing sketch id3333_RECICLANDO_BASURA__DIGITALMENTE_0 (saved by Fritzing 0.9.3b)

parts:
  Parte1 = Arduino Uno (Rev3)
  LED1 = smd LED [color="Red (633nm)" package="1206 [SMD]"]
  Parte4 = bluetooth-module
  J1 = Basic Servo

nets:
  N1: Parte1.D13/SCK, J1.pulse
  GND: Parte1.GND, LED1.cathode, Parte4.connector14, J1.gnd
  N2: Parte1.D0/RX, Parte4.connector15
  N3: Parte1.D1/TX, Parte4.connector16
  N4: Parte1.D5_PWM, LED1.anode
  5V: Parte1.5V, Parte4.connector13, J1.vcc
