# Fritzing sketch id3335_LVDT1_0 (saved by Fritzing 0.8.7b)
circuit board: 8.46667cm x 5.64444cm
breadboards: 2

parts:
  LM837 = IC, DIP package, 14 pins [chip_label=LM837 part_number=LM837]
  VCC1 = Battery block 9V
  VCC2 = Battery block 9V
  R3 = Resistor [tolerance=±5% resistance=10k part_number=R3 package=THT]
  R4 = Resistor [tolerance=±5% resistance=22k part_number=R4 package=THT]
  R1_1 = Resistor [tolerance=±5% resistance=3.3k part_number=R1 package=THT]
  C1 = Ceramic Capacitor [capacitance=10nF part_number=C1 package="100 mil [THT, multilayer]"]
  C2 = Ceramic Capacitor [capacitance=10nF part_number=C2 package="100 mil [THT, multilayer]"]
  LED1 = LED - 5mm [color="Red (633nm)" package="5 mm [THT]"]
  LED2 = LED - 5mm [color="Green (555nm)" package="5 mm [THT]"]
  RL1 = Resistor [tolerance=±5% resistance=1k package=THT]
  RL2 = Resistor [tolerance=±5% resistance=1k package=THT]
  R1_3 = Resistor [tolerance=±1% resistance=68 package=THT]
  R1_2 = Resistor [tolerance=±1% resistance=3k part_number=R1 package=THT]
  R2_1 = Resistor [tolerance=±5% resistance=3.3k part_number=R2 package=THT]
  R2_2 = Resistor [tolerance=±1% resistance=3k package=THT]
  R2_3 = Resistor [tolerance=±1% resistance=68 part_number=R2 package=THT]
  R6 = Trimmer Potentiometer [maximum_resistance=22kΩ package=THT]
  CF2 = Ceramic Capacitor [capacitance=100nF package="100 mil [THT, multilayer]"]
  RF3_2 = Resistor [tolerance=±5% resistance=150 package=THT]
  CF1 = Ceramic Capacitor [capacitance=100nF package="100 mil [THT, multilayer]"]
  RF3_1 = Resistor [tolerance=±5% resistance=470 package=THT]
  RF5 = Resistor [tolerance=±5% resistance=1k package=THT]
  RF4 = Resistor [tolerance=±5% resistance=470 package=THT]
  L1 = Inductor [package="400 mil [THT]"]
  LM838 = IC, DIP package, 14 pins [chip_label=LM837 part_number=LM837]
  D1 = Rectifier Diode [part_number=1N4001 package="300 mil [THT]"]
  D2 = Rectifier Diode [part_number=1N4001 package="300 mil [THT]"]
  R19 = Resistor [tolerance=±5% resistance=10k package=THT]
  R20 = Resistor [tolerance=±5% resistance=10k package=THT]
  RF2 = Resistor [tolerance=±5% resistance=680 package=THT]

nets (from the breadboard view):
  N1: LM837.pin1, LM837.pin5, R2_3.Pin_1
  N2: LM837.pin2, R3.Pin_1, R4.Pin_1
  N3: LM837.pin3, R1_1.Pin_0, C1.0, C2.1
  N4: LM837.pin4, VCC1.+, RL2.Pin_1, LM838.pin4
  N5: LM837.pin6, LM837.pin7, R6.wiper
  N6: LM837.pin8, LM837.pin12, RF5.Pin_1, RF2.Pin_0
  N7: LM837.pin9, RF5.Pin_0, RF4.Pin_1
  N8: LM837.pin10, CF2.0, RF3_1.Pin_0
  N9: LM837.pin11, VCC2.-, LED1.cathode
  N10: LM837.pin13, LM837.pin14, L1.pin_1, LM838.pin3
  N11: VCC1.-, VCC2.+, R3.Pin_0, C1.1, LED2.cathode, RL1.Pin_1, R1_3.Pin_1, RF3_2.Pin_1, CF1.1, RF4.Pin_0, L1.pin_0
  N12: R1_1.Pin_1, R1_2.Pin_0
  N13: C2.0, R2_1.Pin_0
  N14: LED1.anode, RL1.Pin_0
  N15: LED2.anode, RL2.Pin_0
  N16: R1_3.Pin_0, R1_2.Pin_1
  N17: R2_1.Pin_1, R2_2.Pin_0
  N18: R2_2.Pin_1, R2_3.Pin_0
  N19: R6.leg2, CF2.1, CF1.0, RF2.Pin_1
  N20: RF3_2.Pin_0, RF3_1.Pin_1
  N21: LM838.pin1, LM838.pin2, R19.Pin_1
  N22: D1.cathode, R20.Pin_0
  N23: D1.anode, D2.cathode
  N24: D2.anode, R19.Pin_0, R20.Pin_1
