# Fritzing sketch id3336_Arduino_MITSUMI_Stepper_0 (saved by Fritzing 0.7.10b)
breadboards: 1

parts:
  Arduino1 = Arduino
  M35SP-7N1 = stepper_motor_bipolar.fzp  # not connected
  IC1 = H-Bridge [package=THT]  # not connected
  Power_plug1 = Power plug

nets:
  GND: Arduino1.GND, Power_plug1.GND

notes:
  5 Volts
  M35SP-7N
  bipolar stepper motor recycled from a scanner
  This project uses the
  SN754410 motor driver IC for pilot a recycled stepper motor
