# Fritzing sketch id3338_RedSignal_Karam_0 (saved by Fritzing 0.9.2b)
breadboards: 1

parts:
  U1 = 7-SEGMENT-DISPLAY [package=7-segment-display]
  Part1 = Arduino Uno (Rev3)
  R1 = Resistor [tolerance=±5% resistance=220 package=THT]
  LED1 = LED - 5mm [color="Red (633nm)" package="5 mm [THT]"]
  R2 = Resistor [tolerance=±5% resistance=220 package=THT]
  Part2 = SRF05 Ultrasonic Rangefinder
  R3 = Resistor [tolerance=±5% resistance=561 package=THT]
  LED2 = LED - 5mm [color="Red (633nm)" package="5 mm [THT]"]
  J1 = Piezo Speaker

nets:
  N1: U1.E, Part1.D9_PWM
  N2: U1.D, Part1.D6_PWM
  N3: U1.G1, Part1.D5_PWM
  N4: U1.C, R1.Pin_0
  N5: U1.DP, Part1.D4
  N6: U1.A, Part1.D3_PWM
  N7: U1.G2, Part1.D2
  N8: U1.F, R2.Pin_0
  N9: U1.G, Part1.D8
  N10: Part1.D10_PWM/SS, LED1.anode
  N11: Part1.D12/MISO, Part2.connector10
  N12: Part1.D13/SCK, Part2.connector9
  N13: Part1.GND, R1.Pin_1, LED1.cathode, R2.Pin_1, Part2.connector11, R3.Pin_0, J1.pin1
  N14: Part1.D7, LED2.cathode, J1.pin2
  N15: Part1.5V, Part2.connector8
  N16: R3.Pin_1, LED2.anode
