# Fritzing sketch id333_Girouette_HMC5883L_0 (saved by Fritzing 0.8.7b)

parts:
  R16 = Resistor [tolerance=±5% resistance=470 package=THT]
  LED5 = LED - 5mm [color="Red (633nm)" package="5 mm [THT]"]
  Anémomètre/Girouette1 = Arduino Nano (Rev3.0)
  S2 = Reed switch [package=THT]
  R17 = Resistor [tolerance=±5% resistance=10k package=THT]
  C2 = Ceramic Capacitor [capacitance=100nF package="100 mil [THT, multilayer]"]
  R18 = Resistor [tolerance=±5% resistance=2.2k package=THT]
  HMC5883L1 = Triple Axis Magnetometer - HMC5883 Breakout
  J4 = screw terminal, 4 pins
  R19 = Resistor [tolerance=±5% resistance=4.7k package=THT]
  R20 = Resistor [tolerance=±5% resistance=4.7k package=THT]

nets:
  N1: R16.Pin_0, LED5.cathode
  GND: R16.Pin_1, Anémomètre/Girouette1.GND, R18.Pin_1, HMC5883L1.GND, J4.pin4
  N2: LED5.anode, Anémomètre/Girouette1.D10
  N3: Anémomètre/Girouette1.D1/TX, J4.pin1
  N4: Anémomètre/Girouette1.D0/RX, J4.pin2
  N5: Anémomètre/Girouette1.D2, S2.pin_1, R17.Pin_1, C2.0
  N6: Anémomètre/Girouette1.D4, HMC5883L1.SDA, R20.Pin_1
  N7: Anémomètre/Girouette1.D5, HMC5883L1.SCL, R19.Pin_1
  N8: Anémomètre/Girouette1.5V, R17.Pin_0, J4.pin3
  3V3: Anémomètre/Girouette1.3V3, HMC5883L1.VCC, R19.Pin_0, R20.Pin_0
  N9: S2.pin_2, C2.1, R18.Pin_0
