# Fritzing sketch id3340_LM3915_Stereo_0 (saved by Fritzing 0.9.3b)
circuit board: 7.06066cm x 7.35004cm
breadboards: 1

parts:
  IC1 = prefix_lm3915 [chip_label=IC]
  IC2 = prefix_lm3915 [chip_label=IC]
  C1 = Ceramic Capacitor [capacitance=100nF package="100 mil [THT, multilayer]"]
  C2 = Ceramic Capacitor [capacitance=100nF package="100 mil [THT, multilayer]"]
  C3 = Ceramic Capacitor [capacitance=100nF package="100 mil [THT, multilayer]"]
  C4 = Ceramic Capacitor [capacitance=100nF package="100 mil [THT, multilayer]"]
  C5 = Ceramic Capacitor [capacitance=100nF package="100 mil [THT, multilayer]"]
  C6 = Ceramic Capacitor [capacitance=100nF package="100 mil [THT, multilayer]"]
  C7 = Ceramic Capacitor [capacitance=100nF package="100 mil [THT, multilayer]"]
  C8 = Ceramic Capacitor [capacitance=100nF package="100 mil [THT, multilayer]"]
  C9 = Ceramic Capacitor [capacitance=100nF package="100 mil [THT, multilayer]"]
  C10 = Ceramic Capacitor [capacitance=100nF package="100 mil [THT, multilayer]"]
  C11 = Ceramic Capacitor [capacitance=100nF package="100 mil [THT, multilayer]"]
  C12 = Ceramic Capacitor [capacitance=100nF package="100 mil [THT, multilayer]"]
  C13 = Ceramic Capacitor [capacitance=100nF package="100 mil [THT, multilayer]"]
  C14 = Ceramic Capacitor [capacitance=100nF package="100 mil [THT, multilayer]"]
  C15 = Ceramic Capacitor [capacitance=100nF package="100 mil [THT, multilayer]"]
  C16 = Ceramic Capacitor [capacitance=100nF package="100 mil [THT, multilayer]"]
  C17 = Ceramic Capacitor [capacitance=100nF package="100 mil [THT, multilayer]"]
  C18 = Ceramic Capacitor [capacitance=100nF package="100 mil [THT, multilayer]"]
  C19 = Ceramic Capacitor [capacitance=100nF package="100 mil [THT, multilayer]"]
  C20 = Ceramic Capacitor [capacitance=100nF package="100 mil [THT, multilayer]"]
  R1 = Resistor [tolerance=±5% resistance=220 package=THT]
  R2 = Resistor [tolerance=±5% resistance=220 package=THT]
  R5 = Resistor [tolerance=±5% resistance=220 package=THT]
  R6 = Resistor [tolerance=±5% resistance=220 package=THT]
  R7 = Resistor [tolerance=±5% resistance=220 package=THT]
  R8 = Resistor [tolerance=±5% resistance=220 package=THT]
  R9 = Resistor [tolerance=±5% resistance=220 package=THT]
  R10 = Resistor [tolerance=±5% resistance=220 package=THT]
  R11 = Resistor [tolerance=±5% resistance=220 package=THT]
  R12 = Resistor [tolerance=±5% resistance=220 package=THT]
  R13 = Resistor [tolerance=±5% resistance=220 package=THT]
  R14 = Resistor [tolerance=±5% resistance=220 package=THT]
  R15 = Resistor [tolerance=±5% resistance=220 package=THT]
  R16 = Resistor [tolerance=±5% resistance=220 package=THT]
  C21 = Ceramic Capacitor [capacitance=100nF package="100 mil [THT, multilayer]"]
  C22 = Ceramic Capacitor [capacitance=100nF package="100 mil [THT, multilayer]"]
  R17 = TRIMPOT [package=3386u]
  R18 = TRIMPOT [package=3386u]
  R19 = Resistor [tolerance=±5% resistance=220 package=THT]
  R20 = Resistor [tolerance=±5% resistance=220 package=THT]
  C23 = Ceramic Capacitor [capacitance=100nF package="100 mil [THT, multilayer]"]
  C24 = Ceramic Capacitor [capacitance=100nF package="100 mil [THT, multilayer]"]

nets:
  N1: IC1.connector0, IC1.connector2, IC2.connector2, C1.1, C2.1, C3.1, C4.1, C5.1, C6.1, C7.1, C8.1, C9.1, C10.1, C11.0, C11.1, C12.1, C13.1, C14.1, C15.1, C16.1, C17.1, C18.1, C19.1, C20.1, R1.Pin_1, R2.Pin_1, R10.Pin_0, R14.Pin_0, C21.0, C22.0
  N2: IC1.connector1, IC1.connector3, IC1.connector7, IC2.connector1, IC2.connector3, IC2.connector7, R6.Pin_1, R8.Pin_1, C21.1, C22.1, R17.CCW, R18.CCW, R19.Pin_1, R20.Pin_1
  N3: IC1.connector4, R17.WIPER
  N4: IC1.connector5, R2.Pin_0, R19.Pin_0
  N5: IC1.connector6, R13.Pin_0
  N6: IC1.connector9, R15.Pin_0
  N7: IC1.connector10, R16.Pin_0
  N8: IC1.connector11, C18.0
  N9: IC1.connector12, C17.0
  N10: IC1.connector13, C16.0
  N11: IC1.connector14, C15.0
  N12: IC1.connector15, C14.0
  N13: IC1.connector16, C13.0
  N14: IC1.connector17, C12.0
  N15: IC2.connector0, C1.0
  N16: IC2.connector4, R18.WIPER
  N17: IC2.connector5, R1.Pin_0, R20.Pin_0
  N18: IC2.connector6, R9.Pin_0
  N19: IC2.connector9, R11.Pin_0
  N20: IC2.connector10, R12.Pin_0
  N21: IC2.connector11, C8.0
  N22: IC2.connector12, C7.0
  N23: IC2.connector13, C6.0
  N24: IC2.connector14, C5.0
  N25: IC2.connector15, C4.0
  N26: IC2.connector16, C3.0
  N27: IC2.connector17, C2.0
  N28: C9.0, R12.Pin_1
  N29: C10.0, R11.Pin_1
  N30: C19.0, R16.Pin_1
  N31: C20.0, R15.Pin_1
  N32: R5.Pin_1, R17.CW
  N33: R7.Pin_1, R18.CW
  N34: R9.Pin_1, C24.0
  N35: R10.Pin_1, C24.1
  N36: R13.Pin_1, C23.0
  N37: R14.Pin_1, C23.1
