# Fritzing sketch id3342_Regolith_0 (saved by Fritzing 0.9.3b)
circuit board: 8.46667cm x 5.64444cm

parts:
  Componente2 = Arduino Uno (Rev3) - ICSP
  RHT1 = Humidity and Temperature Sensor RHT03
  LED1 = RGB LED (com. cathode, rbg) [package="5 mm [THT]"]

nets:
  N1: Componente2.GND, RHT1.GND_1, LED1.common_cathode
  N2: Componente2.D3_PWM, LED1.blue_anode
  N3: Componente2.D5_PWM, LED1.green_anode
  N4: Componente2.D6_PWM, LED1.red_anode
  N5: Componente2.D7, RHT1.Data-signal
  5V: Componente2.5V, RHT1.Vcc
