# Fritzing sketch id3343_regulador_0 (saved by Fritzing 0.9.2b)
circuit board: 5.3049cm x 4.39027cm
breadboards: 1

parts:
  J1 = Power Jack [package=power_jack_slot]
  7805 = Voltage Regulator - 5V [package="TO220 [THT]"]
  S1 = Pushbutton [package=THT]
  S2 = SPST Switch [package=switch-spdt_kit]
  C1 = Electrolytic Capacitor [capacitance=10µF voltage=20V package="100 mil [THT, electrolytic]"]
  C2 = Electrolytic Capacitor [capacitance=1µF package="100 mil [THT, electrolytic]"]
  C3 = Ceramic Capacitor [capacitance=100nF package="100 mil [THT, multilayer]"]
  LED1 = LED - 5mm [color="Green (570nm)" package="5 mm [THT]"]
  R1 = Resistor [tolerance=±5% resistance=220 package=THT]
  5V = Header 1 [package=1x01_offset]
  GND = Header 1 [package=1x01_offset]
  7809 = Voltage Regulator - 5V [package="TO220 [THT]"]
  C4 = Electrolytic Capacitor [capacitance=1µF package="100 mil [THT, electrolytic]"]
  C5 = Ceramic Capacitor [capacitance=100nF package="100 mil [THT, multilayer]"]
  LED2 = LED - 5mm [color="Green (570nm)" package="5 mm [THT]"]
  R2 = Resistor [tolerance=±5% resistance=220 package=THT]
  9V = Header 1 [package=1x01_offset]

nets:
  GND: J1.GND, 7805.GND, C1.-, C2.-, C3.0, R1.Pin_1, GND.1, 7809.GND, C4.-, C5.0, R2.Pin_1
  N1: J1.PWR, S1.leg0
  N2: 7805.input_voltage, S2.O
  N3: 7805.output_voltage, C2.+, C3.1, LED1.anode, 5V.1
  N4: S1.leg1, S2.P, C1.+
  N5: S2.S, 7809.input_voltage
  N6: LED1.cathode, R1.Pin_0
  N7: 7809.output_voltage, C4.+, C5.1, LED2.anode, 9V.1
  N8: LED2.cathode, R2.Pin_0

notes:
  Mircomola
  V.H.M.J.
