# Fritzing sketch id3344_regulador_de_led_0 (saved by Fritzing 0.7.5b)
breadboards: 1

parts:
  Arduino1 = Arduino
  Q1 = NPN-Transistor [package="TO92 [THT]"]
  Q2 = NPN-Transistor [package="TO92 [THT]"]
  Q3 = NPN-Transistor [package="TO92 [THT]"]
  R1 = Resistor [tolerance=±5% resistance=220 package=THT]
  R2 = Resistor [tolerance=±5% resistance=220 package=THT]
  R3 = Resistor [tolerance=±5% resistance=220 package=THT]
  D1 = Rectifier Diode [part_number=1N4001 package="300 mil [THT]"]
  D2 = Rectifier Diode [part_number=1N4001 package="300 mil [THT]"]
  D3 = Rectifier Diode [part_number=1N4001 package="300 mil [THT]"]
  LED1 = LED - 5mm [color="Red (633nm)" package="5 mm [THT]"]
  VCC1 = Battery

nets:
  N1: Arduino1.GND, Q1.E, Q2.E
  N2: Arduino1.D7, R1.Pin_0
  N3: Arduino1.D6, R2.Pin_0
  N4: Arduino1.D5, R3.Pin_0
  N5: Q1.B, R1.Pin_1
  N6: Q1.C, D1.cathode
  N7: Q2.B, R2.Pin_1
  N8: Q2.C, D2.cathode
  N9: Q3.E, VCC1.-
  N10: Q3.B, R3.Pin_1
  N11: Q3.C, D3.cathode
  N12: D1.anode, D2.anode, D3.anode, LED1.cathode
  N13: LED1.anode, VCC1.+
