# Fritzing sketch id3345_test_0 (saved by Fritzing 0.9.0b)
breadboards: 1

parts:
  Raspberry_Pi1 = Raspberry Pi B rev2
  U2 = RELAY [package=relay-jzc]
  U1 = RELAY [package=relay-jzc]
  VCC1 = Battery block 9V
  LED1 = smd LED [color="Red (633nm)" package="0805 [SMD]"]
  LED2 = smd LED [color="Red (633nm)" package="0805 [SMD]"]

nets:
  N1: Raspberry_Pi1.5V, U2.NO, U1.NO
  N2: Raspberry_Pi1.GND, U2.COIL2, U1.COIL2
  N3: Raspberry_Pi1.GPIO_23, U2.NC
  N4: Raspberry_Pi1.GPIO_18, U1.NC
  N5: U2.MAIN, U1.MAIN, VCC1.-
  N6: U2.COIL1, LED1.cathode
  N7: U1.COIL1, LED2.cathode
  N8: VCC1.+, LED1.anode, LED2.anode
