# Fritzing sketch id3346_Relay_Breakout_0 (saved by Fritzing 0.7.0b)
breadboards: 1

parts:
  R1 = Resistor [tolerance=±5% resistance=220 package=THT]
  LED1 = LED - 5mm [color="Red (633nm)" package="5 mm [THT]"]
  RELAY = Componente_sem_nome
  J3 = screw terminal, 2 pins
  J1 = screw terminal, 2 pins
  J2 = screw terminal, 2 pins
  D1 = Rectifier Diode [part_number=1N4007 package="300 mil [THT]"]

nets:
  N1: R1.Pin_0, RELAY.connector0, J3.pin1, J3.pin2, D1.cathode
  N2: R1.Pin_1, LED1.anode
  N3: LED1.cathode, RELAY.connector1, J2.pin2, D1.anode
  N4: RELAY.connector2, J2.pin1
  N5: RELAY.connector3, J1.pin1
  N6: RELAY.connector4, J1.pin2

notes:
  COM
  V+
  GND
  NC NO
  Relay Breakout
  phgbecker
