# Fritzing sketch id3347_1_Relay_motor_reverse_control_0 (saved by Fritzing 0.9.2b)

parts:
  Part1 = Arduino Uno (Rev3)
  U3 = G3VM-61E1 [part_number=Test package=g3vm-61e1]
  U4 = G3VM-61E1 [package=g3vm-61e1]
  U5 = G3VM-61E1 [package=g3vm-61e1]
  U6 = G3VM-61E1 [package=g3vm-61e1]
  M1 = DC Motor  # not connected
  Power_plug1 = Power plug

nets:
  N1: Part1.D9_PWM, U3.P$4
  N2: Part1.D10_PWM/SS, U4.P$4
  N3: Part1.D11_PWM/MOSI, U5.P$4
  N4: Part1.D12/MISO, U6.P$4
  N5: Part1.5V, U3.P$6
  N6: Part1.GND, U3.P$5
  N7: U3.P$2, U5.P$2, Power_plug1.VCC
  N8: U4.P$2, U6.P$2, Power_plug1.GND

notes:
  Trigger pins 9 & 10
  Trigger pins 11 & 12
  12V Power source
  this can be a 12v battery or a 12v power supply or charger etc
  Relays 1 and 2 for right direction
  12V DC Motor
  Relays 3 and 4 for right direction
