# Fritzing sketch id3348_Relay_Module_v1_0 (saved by Fritzing 0.9.1b)
circuit board: 4.5cm x 2cm
breadboards: 1

parts:
  Arduino1 = Arduino Uno (Rev3)
  1k = Resistor [tolerance=±5% resistance=1k package=THT]
  10k = Resistor [tolerance=±5% resistance=10k package=THT]
  Q4 = TRANSISTOR_NPN [package=to-92-ammo]
  470 = Resistor [tolerance=±5% resistance=470 package=THT]
  D1 = Rectifier Diode [part_number=1N4148 package="300 mil [THT]"]
  2N3904 = Componente_sem_nome
  J19 = screw terminal, 3 pins
  J20 = female pin header, 3 pins [form="♀ (female)"]
  LED1 = LED - 3mm [color="Red (633nm)" package="3 mm [THT]"]

nets:
  N1: Arduino1.5V, 470.Pin_0, D1.cathode, 2N3904.connector1, J20.pin2
  N2: Arduino1.GND, 10k.Pin_1, Q4.E, J20.pin1
  N3: 1k.Pin_0, J20.pin3
  N4: 1k.Pin_1, 10k.Pin_0, Q4.B
  N5: Q4.C, D1.anode, 2N3904.connector0, LED1.cathode
  N6: 470.Pin_1, LED1.anode
  N7: 2N3904.connector2, J19.pin2
  N8: 2N3904.connector3, J19.pin3
  N9: 2N3904.connector4, J19.pin1

notes:
  In this circuit a 5V relay is connected to the arduino board and controls a AC or DC circuit which is connected to an external power supply.
