# Fritzing sketch id3349_RM_001_0 (saved by Fritzing 0.9.3b)
circuit board: 5cm x 2.3cm
breadboards: 1

parts:
  RELAY = OMRON PCB Power Relay – G5LE [part_number="G5LE-1\n" package=THT]
  D1 = Zener Diode [part_number=1N4732A breakdown_voltage=3.6V package="Melf DO-213 AB [SMD]"]
  Q1 = TRANSISTOR_NPN [package=sot23]
  R2 = Resistor [tolerance=±5% resistance=1k package="0805 [SMD]"]
  R1 = Resistor [tolerance=±5% resistance=1k package="0805 [SMD]"]
  U1 = TLP621 [package=THT]
  J2 = screw terminal, 3 pins
  J1 = male pin header, 3 pins [form="♂ (male)"]

nets:
  N1: RELAY.A, J2.pin3
  N2: RELAY.COIL1, D1.cathode, U1.Pin_4, J1.pin3
  N3: RELAY.C, J2.pin2
  N4: RELAY.COIL2, D1.anode, Q1.C
  N5: RELAY.B, J2.pin1
  N6: Q1.B, R2.Pin_0
  N7: Q1.E, U1.Pin_2, J1.pin1
  N8: R2.Pin_1, U1.Pin_3
  N9: R1.Pin_0, J1.pin2
  N10: R1.Pin_1, U1.Pin_1

notes:
  GND
  VCC
  IN
  NC
  NO
  COM
