# Fritzing sketch id334_NWT_2018_0 (saved by Fritzing 0.9.3b)
breadboards: 1

parts:
  R1 = Resistor [tolerance=±5% resistance=10k package=THT]
  R2 = Resistor [tolerance=±5% resistance=10k package=THT]
  Bauteil1 = Arduino Uno (Rev3)
  R3 = Photocell (LDR) [package=THT]
  R4 = Photocell (LDR) [package=THT]
  J1 = Basic Servo

nets:
  N1: R1.Pin_0, R4.pin_1
  GND: R1.Pin_1, R2.Pin_1, Bauteil1.GND, J1.gnd
  N2: R2.Pin_0, R3.pin_1
  5V: Bauteil1.A0, Bauteil1.A1, Bauteil1.5V, R3.pin_0, R4.pin_0, J1.vcc
  N3: Bauteil1.D6_PWM, J1.pulse
