# Fritzing sketch id3350_rele2_0 (saved by Fritzing 0.9.2b)
circuit board: 5.373cm x 5.48589cm

parts:
  Relay2 = Relay_T73
  Relay3 = Relay_T73
  Relay4 = Relay_T73
  U1 = atmega328 [package=dip]
  D1 = Diode [package=diode-1n4148]
  D2 = Diode [package=diode-1n4148]
  D3 = Diode [package=diode-1n4148]
  Q2 = TRANSISTOR_NPN [package=to-92-ammo]
  Q3 = TRANSISTOR_NPN [package=to-92-ammo]
  Q4 = TRANSISTOR_NPN [package=to-92-ammo]
  R1 = Resistor [tolerance=±5% resistance=220 package=THT]
  R2 = Resistor [tolerance=±5% resistance=220 package=THT]
  R3 = Resistor [tolerance=±5% resistance=220 package=THT]
  J2 = screw terminal, 3 pins
  J3 = screw terminal, 3 pins
  J4 = screw terminal, 3 pins
  XTAL1 = Crystal [frequency="16 Mhz" package=THT]
  C1 = Capacitor [package=cap-pth-small2]
  C2 = Capacitor [package=cap-pth-small2]
  U2 = V_REG_LD1117VXX [package=78xxl]
  JP2 = Header 5x2 [package=2x5-raf]

nets:
  N1: Relay2.connector0, D1.A, Q4.C
  N2: Relay2.connector1, Relay3.connector1, Relay4.connector1, U1.VCC, U1.AVCC, D1.C, D2.C, D3.C, U2.IN, JP2.10
  N3: Relay2.connector2, J2.pin2
  N4: Relay2.connector3, J2.pin3
  N5: Relay2.connector4, J2.pin1
  N6: Relay3.connector0, D2.A, Q3.C
  N7: Relay3.connector2, J3.pin2
  N8: Relay3.connector3, J3.pin3
  N9: Relay3.connector4, J3.pin1
  N10: Relay4.connector0, D3.A, Q2.C
  N11: Relay4.connector2, J4.pin2
  N12: Relay4.connector3, J4.pin3
  N13: Relay4.connector4, J4.pin1
  N14: U1.D2, R1.Pin_1
  N15: U1.D3_(PWM), R2.Pin_1
  N16: U1.D4, R3.Pin_1
  GND: U1.GND, Q2.E, Q3.E, Q4.E, C1.1, C2.1, U2.GND, JP2.1, JP2.9
  N17: U1.XLAT1, XTAL1.pin_1, C2.2
  N18: U1.XLAT2, XTAL1.pin_0, C1.2
  N19: U1.D9_(PWM), JP2.3
  N20: U1.D10_(PWM), JP2.4
  N21: U1.D11_(PWM), JP2.6
  N22: U1.D12, JP2.7
  N23: U1.D13, JP2.5
  N24: Q2.B, R1.Pin_0
  N25: Q3.B, R2.Pin_0
  N26: Q4.B, R3.Pin_0
  N27: U2.OUT, JP2.2
