# Fritzing sketch id3351_relay_test_circuit_0 (saved by Fritzing 0.9.2b)
breadboards: 1

parts:
  Part1 = Arduino Uno (Rev3)
  K1 = Relay [part_number=FRS1B-S package=THT]
  Q1 = NPN-Transistor [package="TO92 [THT]"]
  R1 = Resistor [tolerance=±5% resistance=330 package=THT]
  D1 = Rectifier Diode [part_number=1N4001 package="300 mil [THT]"]
  LED1 = LED - 5mm [color="Red (633nm)" package="5 mm [THT]"]
  LED2 = LED - 5mm [color="Yellow (595nm)" package="5 mm [THT]"]

nets:
  N1: Part1.GND, Q1.C, LED1.cathode, LED2.cathode
  N2: Part1.D2, R1.Pin_1
  N3: Part1.5V, K1.COIL2, D1.cathode
  N4: K1.A, LED1.anode
  N5: K1.COIL1, Q1.E, D1.anode
  N6: K1.C1, K1.C2
  N7: K1.B, LED2.anode
  N8: Q1.B, R1.Pin_0
