# Fritzing sketch id3352_RelayPilot3_0 (saved by Fritzing 0.9.2b)
circuit board: 4.98302cm x 3.21381cm

parts:
  D1 = Diode [package=diode-1n4148]
  D2 = Diode [package=diode-1n4148]
  T1 = NPN-Transistor [part_number=T1 package="TO92 [THT]"]
  JP3 = Header 2 [package=screwterminal-3.5mm-2_lock]
  RelIn = Header 2 [package=screwterminal-3.5mm-2_lock]
  Phase = Header 2 [package=screwterminal-3.5mm-2_lock]
  R3 = Resistor [tolerance=±5% resistance=1k package=THT]
  R1 = Resistor [tolerance=±5% resistance=5k part_number=R1 package=THT]
  J4 = female pin header, 6 pins [form="♀ (female)"]
  Out = female pin header, 6 pins [form="♀ (female)"]
  R2 = Resistor [tolerance=±5% resistance=5k part_number=R2 package=THT]
  R4 = Resistor [tolerance=±5% resistance=1k package=THT]
  T2 = NPN-Transistor [part_number=T2 package="TO92 [THT]"]
  MCU = female pin header, 15 pins [form="♀ (female)"]
  NodeMCU = female pin header, 15 pins [form="♀ (female)"]

nets:
  N1: D1.A, D2.C, JP3.2
  N2: D1.C, RelIn.2
  N3: D2.A, RelIn.1
  N4: T1.E, T2.E, NodeMCU.pin8
  N5: T1.B, R1.Pin_0
  N6: T1.C, J4.pin6, R4.Pin_1
  N7: JP3.1, Phase.1, Phase.2
  N8: R3.Pin_0, J4.pin1, J4.pin2, R4.Pin_0, NodeMCU.pin15
  N9: R3.Pin_1, J4.pin5, T2.C
  N10: R1.Pin_1, MCU.pin10
  N11: J4.pin3, J4.pin4, NodeMCU.pin14
  N12: Out.pin1, MCU.pin2
  N13: Out.pin2, MCU.pin3
  N14: Out.pin3, MCU.pin4
  N15: Out.pin4, MCU.pin5
  N16: Out.pin5, MCU.pin7
  N17: Out.pin6, MCU.pin6
  N18: R2.Pin_0, T2.B
  N19: R2.Pin_1, MCU.pin11

notes:
  Sortie fil pilote
  Phase 220v
  PhaseIN
  RelayPilot Rev 2
  D1
  D2
  D3
  D4
  3V3
  Gnd
  5V
  O2
  O1
  230V!
