# Fritzing sketch id3355_Keypad_rele_Sketch_micro_v4_0 (saved by Fritzing 0.8.5b)

parts:
  Part1 = Arduino Micro (Rev3)
  U1 = RELAY [package=relay-jzc]
  U2 = RELAY [package=relay-jzc]
  U3 = RELAY [package=relay-jzc]
  U4 = RELAY [package=relay-jzc]
  U5 = LCD-16X2 [package=lcd-16x2]
  S1 = Square Pushbutton
  S2 = Square Pushbutton
  S3 = Square Pushbutton
  X2 = DB9 Connector [package=db9]
  XLR1 = XLR3_NCFAH2 [package=xlr3_nc3fah2]
  S4 = SPST Switch [package=switche-dpdt]
  S5 = Square Pushbutton

nets:
  N1: Part1.RESET, U1.MAIN, U3.MAIN, U4.MAIN, S1.leg1
  N2: Part1.GND, U1.COIL1, U5.K
  N3: Part1.D2/SDA, U2.COIL1
  N4: Part1.D3/SCL, U3.COIL1
  N5: Part1.D4_PWM/A6, U4.COIL1
  N6: Part1.D7, S5.leg0
  N7: Part1.D10_PWM/A10, S3.leg0
  N8: Part1.D11_PWM, S2.leg0
  N9: Part1.D12_PWM/A11, S1.leg0
  N10: Part1.5V, U5.A
  N11: Part1.A5, U5.VDD
  N12: Part1.A4, U5.VSS
  N13: U1.COIL2, XLR1.G
  N14: U1.NC, X2.7
  N15: U2.NC, X2.6
  N16: U3.COIL2, S4.P
  N17: U3.NC, X2.5
  N18: U3.NO, X2.4
  N19: U4.COIL2, X2.3
  N20: U4.NC, X2.2
  N21: U4.NO, X2.1
  N22: X2.9, XLR1.3

notes:
  12 VCC
  connector with
  dip switch for select kind of signal (vcc or gnd)
  DB9
  LCD 16x2
  MENU 1
  riga 1) "voce 1"
  riga 2) valore
  MENU 2
  riga 1) "voce 2"
  riga 2) valore ms
  MENU 3
  riga 1) "voce 3"
  riga 2) valore ms
  MENU 4
  riga 1) "voce 4"
  riga 2) valore
  Change menu
  Value +
  Value -
  SHOT
  Rele 1 - Rele 2 - Rele 3 - Rele 4
