# Fritzing sketch id3357_placa1_0 (saved by Fritzing 0.9.2b)
circuit board: 6.95527cm x 5.4058cm
breadboards: 1

parts:
  LED1 = LED - 3mm [color="Red (633nm)" package="3 mm [THT]"]
  LED2 = LED - 3mm [color="Red (633nm)" package="3 mm [THT]"]
  LED3 = LED - 3mm [color="Red (633nm)" package="3 mm [THT]"]
  LED4 = LED - 3mm [color="Red (633nm)" package="3 mm [THT]"]
  LED5 = LED - 3mm [color="Red (633nm)" package="3 mm [THT]"]
  LED6 = LED - 3mm [color="Red (633nm)" package="3 mm [THT]"]
  R1 = Resistor [tolerance=±5% resistance=220 package=THT]
  LED8 = LED - 3mm [color="Red (633nm)" package="3 mm [THT]"]
  LED9 = LED - 3mm [color="Red (633nm)" package="3 mm [THT]"]
  LED10 = LED - 3mm [color="Red (633nm)" package="3 mm [THT]"]
  LED11 = LED - 3mm [color="Red (633nm)" package="3 mm [THT]"]
  Parte2 = Real Time Clock Module - DS1307 RTC Breakout Board
  LED7 = LED - 3mm [color="Red (633nm)" package="3 mm [THT]"]
  Parte1 = Arduino Uno (Rev3) - ICSP

nets:
  N1: LED1.cathode, LED2.cathode, LED3.cathode, LED4.cathode, LED5.cathode, LED6.cathode, R1.Pin_1, LED8.cathode, LED9.cathode, LED10.cathode, LED11.cathode, LED7.cathode
  N2: LED1.anode, Parte1.D11_PWM/MOSI
  N3: LED2.anode, Parte1.D10_PWM/SS
  N4: LED3.anode, Parte1.D9_PWM
  N5: LED4.anode, Parte1.D8
  N6: LED5.anode, Parte1.D7
  N7: LED6.anode, Parte1.D6_PWM
  N8: R1.Pin_0, Parte2.SDA, Parte1.GND
  N9: LED8.anode, Parte1.D4
  N10: LED9.anode, Parte1.D3_PWM
  N11: LED10.anode, Parte1.D2
  N12: LED11.anode, Parte1.D12/MISO
  N13: Parte2.GND, Parte1.A5/SCL
  N14: Parte2.SQW, Parte1.A4/SDA
  N15: Parte2.SCL, Parte1.5V
  N16: LED7.anode, Parte1.D5_PWM
