# Fritzing sketch id3359_RelojBin_0 (saved by Fritzing 0.9.3b)
breadboards: 2

parts:
  LED1 = smd LED [color="Red (633nm)" package="0805 [SMD]"]
  LED2 = smd LED [color="Red (633nm)" package="0805 [SMD]"]
  LED3 = smd LED [color="Red (633nm)" package="0805 [SMD]"]
  LED4 = smd LED [color="Red (633nm)" package="0805 [SMD]"]
  LED5 = smd LED [color="Red (633nm)" package="0805 [SMD]"]
  LED6 = smd LED [color="Red (633nm)" package="0805 [SMD]"]
  LED7 = smd LED [color="Red (633nm)" package="0805 [SMD]"]
  LED8 = smd LED [color="Red (633nm)" package="0805 [SMD]"]
  LED9 = smd LED [color="Red (633nm)" package="0805 [SMD]"]
  LED10 = smd LED [color="Red (633nm)" package="0805 [SMD]"]
  LED11 = smd LED [color="Red (633nm)" package="0805 [SMD]"]
  LED12 = smd LED [color="Red (633nm)" package="0805 [SMD]"]
  LED13 = smd LED [color="Red (633nm)" package="0805 [SMD]"]
  R1 = Resistor [tolerance=±5% resistance=220 package="2512 [SMD]"]
  R2 = Resistor [tolerance=±5% resistance=220 package="2512 [SMD]"]
  R3 = Resistor [tolerance=±5% resistance=220 package="2512 [SMD]"]
  R4 = Resistor [tolerance=±5% resistance=220 package="2512 [SMD]"]
  R5 = Resistor [tolerance=±5% resistance=220 package="2512 [SMD]"]
  R6 = Resistor [tolerance=±5% resistance=220 package="2512 [SMD]"]
  R7 = Resistor [tolerance=±5% resistance=220 package="2512 [SMD]"]
  R8 = Resistor [tolerance=±5% resistance=220 package="2512 [SMD]"]
  R9 = Resistor [tolerance=±5% resistance=220 package="2512 [SMD]"]
  R10 = Resistor [tolerance=±5% resistance=220 package="2512 [SMD]"]
  R11 = Resistor [tolerance=±5% resistance=220 package="2512 [SMD]"]
  R12 = Resistor [tolerance=±5% resistance=220 package="2512 [SMD]"]
  R13 = Resistor [tolerance=±5% resistance=220 package="2512 [SMD]"]
  Componente1 = Arduino Uno (Rev3) - ICSP
  S1 = Square Pushbutton
  Componente2 = Real Time Clock Module - DS1307 RTC Breakout Board

nets:
  GND: LED1.cathode, LED2.cathode, LED3.cathode, LED4.cathode, LED5.cathode, LED6.cathode, LED7.cathode, LED8.cathode, LED9.cathode, LED10.cathode, LED11.cathode, LED12.cathode, LED13.cathode, Componente1.GND, S1.leg1, Componente2.GND
  N1: LED1.anode, R9.Pin_0
  N2: LED2.anode, R10.Pin_0
  N3: LED3.anode, R8.Pin_0
  N4: LED4.anode, R11.Pin_0
  N5: LED5.anode, R12.Pin_0
  N6: LED6.anode, R13.Pin_0
  N7: LED7.anode, R7.Pin_0
  N8: LED8.anode, R6.Pin_0
  N9: LED9.anode, R1.Pin_0
  N10: LED10.anode, R2.Pin_0
  N11: LED11.anode, R3.Pin_0
  N12: LED12.anode, R4.Pin_0
  N13: LED13.anode, R5.Pin_0
  N14: R1.Pin_1, Componente1.D13/SCK
  N15: R2.Pin_1, Componente1.D12/MISO
  N16: R3.Pin_1, Componente1.D11_PWM/MOSI
  N17: R4.Pin_1, Componente1.D10_PWM/SS
  N18: R5.Pin_1, Componente1.D7
  N19: R6.Pin_1, Componente1.D8
  N20: R7.Pin_1, Componente1.D9_PWM
  N21: R8.Pin_1, Componente1.D6_PWM
  N22: R9.Pin_1, Componente1.A1
  N23: R10.Pin_1, Componente1.A2
  N24: R11.Pin_1, Componente1.D5_PWM
  N25: R12.Pin_1, Componente1.D4
  N26: R13.Pin_1, Componente1.A0
  N27: Componente1.A4/SDA, Componente2.SDA
  N28: Componente1.A5/SCL, Componente2.SCL
  N29: Componente1.D2, S1.leg0
  5V: Componente1.5V, Componente2.5V

notes:
  MINUTOS]
  HORA
