# Fritzing sketch id335_figura_1_0 (saved by Fritzing 0.9.3b)
breadboards: 1

parts:
  LED1 = LED - 5mm [color="Red (633nm)" package="5 mm [THT]"]
  Componente1 = Arduino Uno (Rev3)
  R1 = Resistor [tolerance=±5% resistance=220 package=THT]
  LED2 = LED - 5mm [color="Orange (612nm)" package="5 mm [THT]"]
  R2 = Resistor [tolerance=±5% resistance=220 package=THT]

nets:
  N1: LED1.cathode, Componente1.D13/SCK
  N2: LED1.anode, R1.Pin_1
  N3: Componente1.D11_PWM/MOSI, LED2.cathode
  N4: Componente1.RESET, R1.Pin_0, R2.Pin_0
  N5: LED2.anode, R2.Pin_1
