# Fritzing sketch id3360_reloj_con_temometro__Untitled_Sketch_0 (saved by Fritzing 0.7.10b)
breadboards: 1

parts:
  U1 = atmega328 [package=dip]
  Arduino1 = Arduino
  R1 = Resistor [tolerance=±5% resistance=10k package=THT]
  XTAL1 = Crystal [package=THT]
  LCD1 = LCD screen
  R2 = Trimmer Potentiometer [package=THT]
  S3 = Pushbutton [package="[THT]"]
  R3 = Resistor [tolerance=±5% resistance=10k package=THT]
  T1 = LM35 Temperature Sensor [package="TO92 [THT]"]

nets:
  N1: U1.RESET, Arduino1.RST, R1.Pin_0
  N2: U1.D0_(RX), Arduino1.D0RX
  N3: U1.D1_(TX), Arduino1.D1TX
  N4: U1.D2, LCD1.DB7
  N5: U1.D3_(PWM), LCD1.DB6
  N6: U1.D4, LCD1.DB5
  VCC: U1.VCC, U1.AVCC, Arduino1.+5V, R1.Pin_1, LCD1.VDD, R2.leg2, R3.Pin_0, T1.+Vs
  GND: U1.GND, Arduino1.GND, LCD1.VSS, LCD1.R/W, R2.leg1, S3.Pin_1, S3.Pin_2, T1.GND
  N7: U1.XLAT1, XTAL1.pin_1
  N8: U1.XLAT2, XTAL1.pin_0
  N9: U1.D5_(PWM), LCD1.DB4
  N10: U1.D6_(PWM), LCD1.E
  N11: U1.D7, LCD1.RS
  N12: U1.D9_(PWM), T1.Vout
  N13: U1.D13, S3.Pin_3, S3.Pin_4, R3.Pin_1
  N14: LCD1.V0, R2.wiper
