# Fritzing sketch id3361_Final_0 (saved by Fritzing 0.9.3b)
circuit board: 10.6964cm x 7.18939cm
breadboards: 1

parts:
  74HC595 = 74HC595 [package="DIP16 [THT]"]
  74HC595_2 = 74HC595 [package="DIP16 [THT]"]
  74HC595_3 = 74HC595 [package="DIP16 [THT]"]
  74HC595_4 = 74HC595 [package="DIP16 [THT]"]
  J1 = female pin header, 36 pins [form="♀ (female)"]
  R1 = Resistor [tolerance=±5% resistance=220 package=THT]
  R2 = Resistor [tolerance=±5% resistance=220 package=THT]
  R3 = Resistor [tolerance=±5% resistance=220 package=THT]
  R4 = Resistor [tolerance=±5% resistance=220 package=THT]
  Arduio_Nano = Arduino Nano (Rev3.0)
  S1 = Pushbutton [package=THT]
  J2 = female pin header, 7 pins [form="♀ (female)"]
  J3 = female pin header, 5 pins [form="♀ (female)"]
  Componente1 = richardbruneau00

nets:
  N1: 74HC595.Q1, J1.pin35
  N2: 74HC595.Q2, J1.pin34
  N3: 74HC595.Q3, J1.pin33
  N4: 74HC595.Q4, J1.pin32
  N5: 74HC595.Q5, J1.pin31
  N6: 74HC595.Q6, J1.pin30
  N7: 74HC595.Q7, J1.pin29
  GND: 74HC595.GND, 74HC595.OE, 74HC595_2.GND, 74HC595_2.OE, 74HC595_3.GND, 74HC595_3.OE, 74HC595_4.GND, 74HC595_4.OE, R1.Pin_0, R2.Pin_0, R3.Pin_0, R4.Pin_0, Arduio_Nano.GND, S1.leg1, J2.pin2, Componente1.connector21
  N8: 74HC595.Q7', 74HC595_2.DS
  N9: 74HC595.SH_CP, 74HC595_2.SH_CP, 74HC595_3.SH_CP, 74HC595_4.SH_CP, Arduio_Nano.D8
  N10: 74HC595.ST_CP, 74HC595_2.ST_CP, 74HC595_3.ST_CP, 74HC595_4.ST_CP, Arduio_Nano.D11/MOSI
  N11: 74HC595.DS, Arduio_Nano.D10
  N12: 74HC595.Q0, J1.pin36
  VCC: 74HC595.VCC, 74HC595_2.VCC, 74HC595_3.VCC, 74HC595_4.VCC, Arduio_Nano.5V, J2.pin3, Componente1.connector20
  N13: 74HC595_2.Q1, J1.pin26
  N14: 74HC595_2.Q2, J1.pin25
  N15: 74HC595_2.Q3, J1.pin24
  N16: 74HC595_2.Q4, J1.pin23
  N17: 74HC595_2.Q5, J1.pin22
  N18: 74HC595_2.Q6, J1.pin21
  N19: 74HC595_2.Q7, J1.pin20
  N20: 74HC595_2.Q7', 74HC595_3.DS
  N21: 74HC595_2.Q0, J1.pin27
  N22: 74HC595_3.Q1, J1.pin17
  N23: 74HC595_3.Q2, J1.pin16
  N24: 74HC595_3.Q3, J1.pin15
  N25: 74HC595_3.Q4, J1.pin14
  N26: 74HC595_3.Q5, J1.pin13
  N27: 74HC595_3.Q6, J1.pin12
  N28: 74HC595_3.Q7, J1.pin11
  N29: 74HC595_3.Q7', 74HC595_4.DS
  N30: 74HC595_3.Q0, J1.pin18
  N31: 74HC595_4.Q1, J1.pin8
  N32: 74HC595_4.Q2, J1.pin7
  N33: 74HC595_4.Q3, J1.pin6
  N34: 74HC595_4.Q4, J1.pin5
  N35: 74HC595_4.Q5, J1.pin4
  N36: 74HC595_4.Q6, J1.pin3
  N37: 74HC595_4.Q7, J1.pin2
  N38: 74HC595_4.Q0, J1.pin9
  N39: J1.pin1, J1.pin10, J1.pin19, J1.pin28, R1.Pin_1, R2.Pin_1, R3.Pin_1, R4.Pin_1
  N40: Arduio_Nano.D2, S1.leg0
  N41: Arduio_Nano.D3, J2.pin7, Componente1.connector16
  N42: Arduio_Nano.A5, J2.pin5, Componente1.connector18
  N43: Arduio_Nano.A4, J2.pin4, Componente1.connector19
  N44: J2.pin1, Componente1.connector22
  N45: J2.pin6, Componente1.connector17
  N46: J3.pin1, Componente1.connector11
  N47: J3.pin2, Componente1.connector12
  N48: J3.pin3, Componente1.connector13
  N49: J3.pin4, Componente1.connector14
  N50: J3.pin5, Componente1.connector15

notes:
  GND
  Q7
  Q6
  Q5
  Q4
  Q3
  Q2
  Q1
  Q0
