# Fritzing sketch id3362_Reloj_digital_LCD_alarma_ATMEGA328_0 (saved by Fritzing 0.7.10b)
breadboards: 1

parts:
  U1 = atmega328 [package=dip]
  S1 = Pushbutton [package="[THT]"]
  S2 = Pushbutton [package="[THT]"]
  S3 = Pushbutton [package="[THT]"]
  R1 = 10k Ω Resistor [package=THT]
  R2 = 10k Ω Resistor [package=THT]
  R3 = 10k Ω Resistor [package=THT]
  R4 = 10k Ω Resistor [package=THT]
  Q1 = NPN-Transistor [package="TO92 [THT]"]
  J1 = Piezo Speaker
  LCD1 = LCD screen
  R5 = Trimmer Potentiometer [maximum_resistance=10kΩ package=THT]
  XTAL1 = Crystal [package=THT]
  R6 = 10k Ω Resistor [package=THT]

nets:
  N1: U1.RESET, R6.Pin_0
  N2: U1.D2, LCD1.DB7
  N3: U1.D3_(PWM), LCD1.DB6
  N4: U1.D4, LCD1.DB5
  VCC: U1.VCC, U1.AVCC, R1.Pin_0, R2.Pin_0, R3.Pin_0, J1.pin2, LCD1.VDD, R5.leg1, R6.Pin_1
  GND: U1.GND, S1.Pin_1, S1.Pin_2, S2.Pin_1, S2.Pin_2, S3.Pin_1, S3.Pin_2, Q1.E, LCD1.VSS, LCD1.R/W, R5.leg2
  N5: U1.XLAT1, XTAL1.pin_0
  N6: U1.XLAT2, XTAL1.pin_1
  N7: U1.D5_(PWM), LCD1.DB4
  N8: U1.D6_(PWM), LCD1.E
  N9: U1.D7, LCD1.RS
  N10: U1.D8, S1.Pin_3, S1.Pin_4, R1.Pin_1
  N11: U1.D9_(PWM), S2.Pin_3, S2.Pin_4, R2.Pin_1
  N12: U1.D10_(PWM), S3.Pin_3, S3.Pin_4, R3.Pin_1
  N13: U1.D11_(PWM), R4.Pin_0
  N14: R4.Pin_1, Q1.B
  N15: Q1.C, J1.pin1
  N16: LCD1.V0, R5.wiper
