# Fritzing sketch id3363_reloj_simple_LCD_keypad4x4_0 (saved by Fritzing 0.9.2b)
breadboards: 1

parts:
  Parte1 = Arduino Mega 2560 (Rev3)
  U1 = LCD-16X2 [package=lcd-16x2]
  R1 = Rotary Potentiometer (Small) [maximum_resistance=100kΩ package=THT]
  Matrix_keypad1 = CMG

nets:
  N1: Parte1.D13_PWM, U1.RS
  N2: Parte1.D12_PWM, U1.E
  N3: Parte1.D11_PWM, U1.DB4
  N4: Parte1.D10_PWM, U1.DB5
  N5: Parte1.D9_PWM, U1.DB6
  N6: Parte1.D8_PWM, U1.DB7
  5V: Parte1.5V, U1.VDD, U1.A, R1.leg2
  GND: Parte1.GND, U1.VSS, U1.R_W, U1.K, R1.leg1
  N7: Parte1.D0_RX0, Matrix_keypad1.connector25
  N8: Parte1.D1_TX0, Matrix_keypad1.connector26
  N9: Parte1.D2_PWM, Matrix_keypad1.connector27
  N10: Parte1.D3_PWM, Matrix_keypad1.connector28
  N11: Parte1.D4_PWM, Matrix_keypad1.connector29
  N12: Parte1.D5_PWM, Matrix_keypad1.connector30
  N13: Parte1.D6_PWM, Matrix_keypad1.connector31
  N14: Parte1.D7_PWM, Matrix_keypad1.connector32
  N15: U1.VO, R1.wiper

notes:
  /*Código para Arduino
  ----------------------------------
  Reloj Configurable Sencillo con LCD y teclado 4x4
  ----------------------------------
  2015 - Sebastián de los Angeles
  Debería funcionar con un teclado 3x4, realizando las variaciones del caso.
  Este código se basa en los siguientes tutoriales disponibles en
  la página oficial de Arduino ( http://arduino.cc ):
  - Blink withouth delay(): https://www.arduino.cc/en/Tutorial/BlinkWithoutDelay
  por David A. Mellis y modificado por Paul Stoffregen
  - LiquidCrystal - "Hello World!": http://arduino.cc/en/Tutorial/LiquidCrystal
  por Tom Igoe
  */
  //Importar Librerías para el lcd y el teclado
  #include <Keypad.h>
  #include <LiquidCrystal.h>
  LiquidCrystal lcd(13, 12, 11, 10, 9, 8);
  //Variables utilizadas
  int h, m ,s =0;
  unsigned long tiempoPas=0;
  int segundo=1000;
  boolean listo=false;
  //Config del Teclado
  const byte filas=4;
  const byte colum=4;
  char botones[filas][colum]={
  {
  '1','2','3','A' }
  ,
  {
  '4','5','6','B' }
  ,
  {
  '7','8','9','C' }
  ,
  {
  '*','0','#','D' }
  };
  byte pinesFila[filas]={
  0,1,2,3};
  byte pinesColu[colum]={
  4,5,6,7};
  Keypad teclado=Keypad( makeKeymap(botones),pinesFila,pinesColu,filas,colum );
  // ----------------------------
  //Declaración de Funciones
  //numTeclado() se encarga de obtener los números ingresados en el teclado
  // y devolverlas a una variable de tipo int
  int numTeclado()
  {
  int num = 0;
  char key = teclado.getKey();
  while(key != '#')
  {
  switch (key)
  {
  case NO_KEY:
  break;
  case '0': case '1': case '2': case '3': case '4':
  case '5': case '6': case '7': case '8': case '9':
  lcd.print(key);
  num = num * 10 + (key - '0');
  break;
  case '*':
  num = 0;
  lcd.clear();
  break;
  }
  key = teclado.getKey();
  }
  return num;
  }
  //reloj() es la función que se encarga del funcionamiento del reloj
  void reloj(){
  s++;
  if(s>59){
  s=0;
  m++;
  if(m>59){
  m=0;
  h++;
  if(h<23){
  h=0;
  }
  }
  }
  }
  //formato() recibe los datos del reloj y los formatea para que resulten mas
  //agradables a la vista, agregando un 0 delante de los valores menores que 10
  String formato(int num){
  String resultado="";
  if(num<10)
  resultado="0"+String(num);
  else
  resultado=String(num);
  return resultado;
  }
  //configurar() se encarga de establecer la hora exacta del reloj al iniciarse el
  // sistema
  void configurar(){
  lcd.setCursor(0,0);
  lcd.print("Hora:");
  lcd.setCursor(0,1);
  h=numTeclado();
  lcd.clear();
  lcd.setCursor(0,0);
  lcd.print("Minutos:");
  lcd.setCursor(0,1);
  m=numTeclado();
  lcd.clear();
  listo=true;
  }
  void setup() {
  lcd.begin(16,2);
  }
  void loop(){
  unsigned long tiempo=millis();
  if(listo){
  if(tiempo - tiempoPas > segundo) {
  tiempoPas = tiempo;
  reloj();
  }
  String laHora = "--- "+formato(h)+":"+formato(m)+":"+formato(s)+" ---";
  lcd.setCursor(0,0);
  lcd.print(laHora);
  }
  else{
  configurar();
  }
  }
