# Fritzing sketch id3364_RelojSimple_0 (saved by Fritzing 0.9.3b)
breadboards: 1

parts:
  Componente2 = Arduino Mega 2560 (Rev3)
  LCD2 = LCD screen [part_number=1602]  # not connected
  R2 = Rotary Potentiometer (Small) [maximum_resistance=10kΩ package=THT]  # not connected
  ZS-042_RTC1 = ZS-042 RTC Module

nets:
  N1: Componente2.D21/SCL, ZS-042_RTC1.SCL
  N2: Componente2.D20/SDA, ZS-042_RTC1.SDA
