# Fritzing sketch id3365_Reloj_termometro_LCD_0 (saved by Fritzing 0.7.10b)
breadboards: 1

parts:
  LCD1 = LCD screen
  S1 = Pushbutton [package="[THT]"]
  Arduino1 = Arduino
  T1 = LM35 Temperature Sensor [package="TO92 [THT]"]
  C1 = Electrolytic Capacitor [capacitance=100µF package="100 mil [THT, electrolytic]"]

nets:
  GND: LCD1.VSS, LCD1.R/W, Arduino1.GND, T1.GND, C1.-
  VDD: LCD1.VDD, S1.Pin_1, S1.Pin_2, Arduino1.+5V, T1.+Vs
  N1: LCD1.V0, Arduino1.D9, C1.+
  N2: LCD1.RS, Arduino1.D7
  N3: LCD1.E, Arduino1.D6
  N4: LCD1.DB4, Arduino1.D5
  N5: LCD1.DB5, Arduino1.D4
  N6: LCD1.DB6, Arduino1.D3
  N7: LCD1.DB7, Arduino1.D2
  N8: S1.Pin_3, S1.Pin_4, Arduino1.D13
  N9: Arduino1.A0, T1.Vout
