# Fritzing sketch id3366_Progetto_arduino_1_0 (saved by Fritzing 0.9.2b)

parts:
  P1 = Rotary Potentiometer (Small) [maximum_resistance=10kΩ package=THT]
  R2 = Resistor [tolerance=±5% resistance=4.7k package=THT]
  R3 = Resistor [tolerance=±5% resistance=10k package=THT]
  T1 = NPN-Transistor [package="TO92 [THT]"]
  D1 = Rectifier Diode [part_number=1N4007 package="300 mil [THT]"]
  Relè_1 = RELAY [package=relay-jzc]
  Arduino = Arduino Uno (Rev3)
  LCD = LCD screen
  NRF24L01 = shrouded pin header, 8 pins [form="♂ (shrouded male)"]

nets:
  GND: P1.leg1, R3.Pin_1, T1.E, Arduino.GND, LCD.VSS, LCD.R/W, NRF24L01.pin1
  N1: P1.wiper, LCD.V0
  5V: P1.leg2, D1.cathode, Relè_1.COIL2, Arduino.5V, LCD.VDD
  N2: R2.Pin_0, Arduino.D8
  N3: R2.Pin_1, R3.Pin_0, T1.B
  N4: T1.C, D1.anode, Relè_1.COIL1
  N5: Arduino.D9_PWM, NRF24L01.pin3
  N6: Arduino.D10_PWM/SS, NRF24L01.pin4
  N7: Arduino.D11_PWM/MOSI, LCD.E, NRF24L01.pin6
  N8: Arduino.D12/MISO, LCD.RS, NRF24L01.pin7
  N9: Arduino.D13/SCK, NRF24L01.pin5
  N10: Arduino.D2, LCD.DB7
  N11: Arduino.D3_PWM, LCD.DB6
  N12: Arduino.D4, LCD.DB5
  N13: Arduino.D5_PWM, LCD.DB4
  N14: Arduino.3V3, NRF24L01.pin2

notes:
  NRF24L01
