# Fritzing sketch id3367_InfraRed_Reciever_0 (saved by Fritzing 0.8.7b)
breadboards: 1

parts:
  Q1 = PNP-Transistor [part_number=2n3906 package="TO92 [THT]"]
  IR1 = TSOP312.., 314.. [package=THT]
  D1 = Rectifier Diode [part_number=1N4001 package="300 mil [THT]"]
  R1 = Resistor [tolerance=±5% resistance=470 package=THT]
  C1 = Ceramic Capacitor [capacitance=10µF package="100 mil [THT, multilayer]"]
  R2 = Resistor [tolerance=±5% resistance=10k package=THT]
  R3 = Resistor [tolerance=±5% resistance=10k package=THT]
  R4 = Resistor [tolerance=±5% resistance=10k package=THT]
  IC2 = IC, DIP package, 8 pins [chip_label=555]
  C2 = Ceramic Capacitor [capacitance=1µF package="100 mil [THT, multilayer]"]
  R5 = Resistor [tolerance=±5% resistance=220 package=THT]
  C3 = Electrolytic Capacitor [capacitance=1µF package="100 mil [THT, electrolytic]"]
  R6 = Resistor [tolerance=±5% resistance=500k package=THT]
  C4 = Electrolytic Capacitor [capacitance=1µF package="100 mil [THT, electrolytic]"]
  J1 = Piezo Speaker
  R7 = Resistor [tolerance=±5% resistance=101 package=THT]
  VCC1 = Battery block 9V

nets:
  N1: Q1.E, R3.Pin_1, IC2.pin2
  N2: Q1.B, IR1.GND, C1.1, R2.Pin_1
  N3: Q1.C, R4.Pin_1
  N4: IR1.Vs, D1.cathode, R1.Pin_1
  N5: IR1.Data, D1.anode, C1.0, IC2.pin1, C2.1, C3.-, C4.-, R7.Pin_0, VCC1.-
  N6: R1.Pin_0, R2.Pin_0, R3.Pin_0, IC2.pin8, R5.Pin_0, R6.Pin_0, VCC1.+
  N7: IC2.pin3, J1.pin2
  N8: IC2.pin4, R5.Pin_1, C3.+
  N9: IC2.pin5, C2.0
  N10: IC2.pin6, IC2.pin7, R6.Pin_1, C4.+
  N11: J1.pin1, R7.Pin_1
