# Fritzing sketch id3369_SimpleCar1_0 (saved by Fritzing 0.9.3b)
breadboards: 1

parts:
  Part2 = Arduino Motor Shield (Rev3)
  M4 = DC Motor
  M5 = DC Motor
  M6 = DC Motor
  VCC1 = Battery

nets:
  N1: Part2.B-, M4.pin_2
  N2: Part2.B+, M4.pin_1
  N3: Part2.A-, M5.pin_2, M6.pin_2
  N4: Part2.A+, M5.pin_1, M6.pin_1
  N5: Part2.VMOT, VCC1.+
  N6: Part2.GND, VCC1.-

notes:
  Drive board plugs into Arduino
  Battery power are two wires (Black, Red) from base of car chassis.
  Drive Motors
  Drive Board
  Steering Motor
  Drive Motors Front & Rear
  Batterey from under car
  push wires into motor connectors.
  Red - Red / Black - Black
