# Fritzing sketch id336_Angle_and_Distance_Measurement_Device_using_Arduino_0 (saved by Fritzing 0.9.1b)
breadboards: 1

parts:
  U1 = generic_sip_4_300mil.fzp [chip_label=IC]
  Componente1 = Arduino Uno (Rev3)
  LCD1 = LCD screen
  R1 = Rotary Potentiometer (Small) [maximum_resistance=100kΩ package=THT]
  Part1 = Triple Axis Accelerometer Breakout - ADXL335
  S1 = Pushbutton [package="[THT]"]
  R2 = Resistor [tolerance=±5% resistance=10k package=THT]

nets:
  5V: U1.connector0, Componente1.5V, LCD1.VDD, LCD1.LED+, R1.leg1, Part1.VCC, S1.Pin_3, S1.Pin_4
  N1: U1.connector1, Componente1.D6_PWM
  N2: U1.connector2, Componente1.D7
  GND: U1.connector3, Componente1.GND, LCD1.VSS, LCD1.R/W, LCD1.LED-, R1.leg2, Part1.GND, R2.Pin_1
  N3: Componente1.A1, Part1.XOUT
  N4: Componente1.A2, Part1.YOUT
  N5: Componente1.A3, Part1.ZOUT
  N6: Componente1.D11_PWM/MOSI, LCD1.E
  N7: Componente1.D12/MISO, LCD1.RS
  N8: Componente1.D1/TX, S1.Pin_1, S1.Pin_2, R2.Pin_0
  N9: Componente1.D2, LCD1.DB7
  N10: Componente1.D3_PWM, LCD1.DB6
  N11: Componente1.D4, LCD1.DB5
  N12: Componente1.D5_PWM, LCD1.DB4
  N13: LCD1.V0, R1.wiper
