# Fritzing sketch id3370_Remote_Control_DC_Motor_0 (saved by Fritzing 0.9.2b)
breadboards: 1

parts:
  Part1 = Arduino Uno (Rev3)
  Part2 = Bluetooth HC-05 Macho
  IC1 = L293D [package=THT]
  VCC1 = Battery block 9V
  M1 = DC Motor

nets:
  N1: Part1.D9_PWM, IC1.In_1
  N2: Part1.D10_PWM/SS, IC1.In_2
  N3: Part1.D0/RX, Part2.TXD
  N4: Part1.D1/TX, Part2.RXD
  5V: Part1.5V, Part2.VCC
  GND: Part1.GND, Part2.GND
  N5: IC1.Out_1_(_Controlled_by_Enable_1_), M1.pin_2
  GND_2: IC1.0V, VCC1.-
  N6: IC1.Out_2_(_Controlled_by_Enable_1_), M1.pin_1
  N7: IC1.+Vmotor, VCC1.+
