# Fritzing sketch id3371_rolety_0 (saved by Fritzing 0.9.2b)

parts:
  Part2 = Arduino Nano (Rev3.0)
  LM_7806 = Voltage Regulator - 5V [package="DPak [SMD]"]
  Blind_3 = Basic Servo
  Blind_2 = Basic Servo
  Blind_4 = Basic Servo
  Blind_1 = Basic Servo
  R2 = Resistor [tolerance=±5% resistance=10k package="1206 [SMD]"]
  B1B = Pushbutton [package=THT]
  R3 = Resistor [tolerance=±5% resistance=10k package="1206 [SMD]"]
  R4 = Resistor [tolerance=±5% resistance=10k package="1206 [SMD]"]
  R5 = Resistor [tolerance=±5% resistance=10k package="1206 [SMD]"]
  R6 = Resistor [tolerance=±5% resistance=10k package="1206 [SMD]"]
  R7 = Resistor [tolerance=±5% resistance=10k package="1206 [SMD]"]
  B1U = Pushbutton [package=THT]
  B2B = Pushbutton [package=THT]
  B2U = Pushbutton [package=THT]
  B3B = Pushbutton [package=THT]
  B3U = Pushbutton [package=THT]
  B4B = Pushbutton [package=THT]
  B4U = Pushbutton [package=THT]
  R8 = Resistor [tolerance=±5% resistance=10k package="1206 [SMD]"]
  R9 = Resistor [tolerance=±5% resistance=10k package="1206 [SMD]"]
  IR_Receiver = TSOP312.., 314.. [package=THT]

nets:
  GND: Part2.GND, Blind_3.gnd, Blind_2.gnd, Blind_4.gnd, Blind_1.gnd, R2.Pin_1, R3.Pin_1, R4.Pin_1, R5.Pin_1, R6.Pin_1, R7.Pin_1, R8.Pin_1, R9.Pin_1
  N1: Part2.D2, Blind_1.pulse
  N2: Part2.D3, Blind_2.pulse
  N3: Part2.D4, R2.Pin_0, B1B.leg0
  N4: Part2.D5, R3.Pin_0, B1U.leg1
  N5: Part2.D6, R4.Pin_0, B2B.leg0
  N6: Part2.D7, R5.Pin_0, B2U.leg0
  N7: Part2.D8, Blind_3.pulse
  N8: Part2.D9, Blind_4.pulse
  N9: Part2.D10, R6.Pin_0, B3B.leg0
  N10: Part2.D11/MOSI, IR_Receiver.Data
  N11: Part2.D12/MISO, R7.Pin_0, B3U.leg0
  VCC: Part2.VIN, LM_7806.output_voltage, Blind_3.vcc, Blind_2.vcc, Blind_4.vcc, Blind_1.vcc
  N12: Part2.5V, B1B.leg1, B1U.leg0, B2B.leg1, B2U.leg1, B3B.leg1, B3U.leg1, B4B.leg1, B4U.leg1, IR_Receiver.Vs
  N13: Part2.A1, B4U.leg0, R9.Pin_0
  N14: Part2.A0, B4B.leg0, R8.Pin_0
  GND_2: LM_7806.GND, IR_Receiver.GND
