# Fritzing sketch id3372_remote_light_scheme_0 (saved by Fritzing 0.9.3b)
breadboards: 1

parts:
  S1 = Pushbutton [package="[THT]"]
  CONN1 = USB connector [package=THT]
  LED1 = RGB LED (com. cathode, rgb) [package="5 mm [THT]"]  # not connected
  J1 = Piezo Speaker  # not connected
  Part1 = Spark Core (v1.0)  # not connected

nets:
  N1: S1.Pin_1, S1.Pin_2
  N2: S1.Pin_3, S1.Pin_4
  N3: CONN1.5V, CONN1.d+
  N4: CONN1.d-, CONN1.GND, CONN1.chassis5, CONN1.chassis6

notes:
  This holds the space for the buzzer or could replace it.
  These are the needed components except the transistors, and/ or resistors, etc.
