# Fritzing sketch id3373_Schematic_Diagram_0 (saved by Fritzing 0.9.3b)
breadboards: 1

parts:
  LED1 = LED - 5mm [color="Red (633nm)" package="5 mm [THT]"]
  R1 = Resistor [tolerance=±5% resistance=330 package=THT]  # not connected
  R2 = Resistor [tolerance=±5% resistance=330 package=THT]  # not connected
  LED2 = LED - 5mm [color="Red (633nm)" package="5 mm [THT]"]
  Washer = TMP36 [part_number="vibration sensor" package=to-92-kit]
  Dryer = TMP36 [part_number="vibration sensor" package=to-92-kit]
  part = Raspberry Pi 3 [part_number=RPI-3-V1.2]

nets:
  GND: LED1.cathode, LED2.cathode, Washer.GND, Dryer.GND, part.GND
  VCC: Washer.VCC, Dryer.VCC, part.3v3, part.3V3
  N1: Washer.VOUT, part.GIPO17
  N2: Dryer.VOUT, part.GIPO27
