# Fritzing sketch id3374_vibration_sensor_wiring_0 (saved by Fritzing 0.9.3b)
breadboards: 1

parts:
  R3 = Resistor [tolerance=±5% resistance=220 package=THT]
  R1 = Resistor [tolerance=±5% resistance=220 package=THT]
  LED3 = LED - 5mm [color="Red (633nm)" package="5 mm [THT]"]  # not connected
  Sensor_2_-_Dryer = TMP36 [package=to-92-kit]
  Raspberry_Pi_1 = Raspberry Pi 3 [part_number=RPI-3-V1.2]
  LED2 = LED - 5mm [color="Red (633nm)" package="5 mm [THT]"]
  V = DC Power [voltage=5]  # not connected
  Sensor_1_-_Washer1 = TMP36 [package=to-92-kit]
  V_2 = DC Power [voltage=5]  # not connected

nets:
  N1: R3.Pin_0, Sensor_2_-_Dryer.VOUT, Raspberry_Pi_1.GPIO27
  N2: R3.Pin_1, LED2.anode
  N3: R1.Pin_0, Raspberry_Pi_1.GPIO17, Sensor_1_-_Washer1.VOUT
  VCC: Sensor_2_-_Dryer.VCC, Raspberry_Pi_1.3v3, Sensor_1_-_Washer1.VCC
  GND: Sensor_2_-_Dryer.GND, Raspberry_Pi_1.GND, LED2.cathode, Sensor_1_-_Washer1.GND
