# Fritzing sketch id3375_sesli_renk_okuyan_robot_0 (saved by Fritzing 0.9.1b)
breadboards: 1

parts:
  IC1 = IC, DIP package, 16 pins [chip_label=WTV020-SD]
  Arduino1 = Arduino
  SPKR1 = Loudspeaker
  SENSOR3 = TCS34725

nets:
  N1: IC1.pin1, Arduino1.D13, Arduino1.+5V
  N2: IC1.pin4, SPKR1.pin2
  N3: IC1.pin5, SPKR1.pin1
  N4: IC1.pin7, Arduino1.D11
  N5: IC1.pin8, Arduino1.GND, SENSOR3.connector6
  N6: IC1.pin10, Arduino1.D12
  N7: IC1.pin15, Arduino1.D10
  N8: IC1.pin16, Arduino1.3V3, SENSOR3.connector5
  N9: Arduino1.A4, SENSOR3.connector3
  N10: Arduino1.A5, SENSOR3.connector4

notes:
  1
  16
  8
  9
  Duemilanove
