# Fritzing sketch id3377_Mp3_0 (saved by Fritzing 0.7.7b)
breadboards: 1
stripboards: 1

parts:
  LCD1 = LCD screen
  Arduino1 = Arduino
  R1 = Resistor [tolerance=±5% resistance=220 package=THT]
  R3 = Resistor [tolerance=±5% resistance=3.3k package=THT]
  R5 = Resistor [tolerance=±5% resistance=2.2k package=THT]
  ENCODER = Rotary Encoder [package=THT]
  S1 = Pushbutton [part_number=Adelante package="[THT]"]
  S2 = Pushbutton [part_number=Atrás package="[THT]"]
  R6 = Resistor [tolerance=±5% resistance=2.2k package=THT]
  R7 = Resistor [tolerance=±5% resistance=3.3k package=THT]
  J1 = shrouded pin header, 10 pins [form="♂ (shrouded male)"]
  R8 = Resistor [tolerance=±5% resistance=2.2k package=THT]
  R9 = Resistor [tolerance=±5% resistance=3.3k package=THT]
  R10 = Resistor [tolerance=±5% resistance=2.2k package=THT]
  R11 = Resistor [tolerance=±5% resistance=3.3k package=THT]
  R12 = Resistor [tolerance=±5% resistance=2.2k package=THT]
  R13 = Resistor [tolerance=±5% resistance=3.3k package=THT]
  R14 = Resistor [tolerance=±5% resistance=2.2k package=THT]
  R15 = Resistor [tolerance=±5% resistance=3.3k package=THT]
  J2 = shrouded pin header, 6 pins [form="♂ (shrouded male)"]
  R16 = Trimmer Potentiometer [maximum_resistance=10kΩ package=THT]

nets:
  GND: LCD1.VSS, LCD1.R/W, LCD1.LED-, Arduino1.GND, ENCODER.EncoderPinC
  VDD: LCD1.VDD, Arduino1.+5V, R1.Pin_0, R16.leg2
  N1: LCD1.V0, R16.wiper
  N2: LCD1.RS, Arduino1.D3
  N3: LCD1.E, Arduino1.D4
  N4: LCD1.DB3, LCD1.DB4, Arduino1.A0
  N5: LCD1.DB5, Arduino1.A1
  N6: LCD1.DB6, Arduino1.A2
  N7: LCD1.DB7, Arduino1.A3
  N8: LCD1.LED+, R1.Pin_1
  N9: Arduino1.D13, R14.Pin_1
  N10: Arduino1.D12, J1.pin3, J2.pin3
  N11: Arduino1.D11, R10.Pin_1
  N12: Arduino1.D10, ENCODER.EncoderPinA
  N13: Arduino1.D9, R6.Pin_1
  N14: Arduino1.D8, ENCODER.EncoderPinB
  N15: Arduino1.D7, R8.Pin_1
  N16: Arduino1.D6, R5.Pin_1
  N17: Arduino1.D5, R12.Pin_1
  N18: Arduino1.D2, J1.pin8
  N19: Arduino1.D1TX, S2.Pin_1, S2.Pin_2
  N20: Arduino1.D0RX, S1.Pin_1, S1.Pin_2
  N21: Arduino1.3V3, J1.pin1, J2.pin1
  N22: R3.Pin_1, R5.Pin_0, J1.pin6
  N23: S1.Pin_3, S1.Pin_4, S2.Pin_3, S2.Pin_4
  N24: R7.Pin_0, J2.pin5
  N25: J1.pin2, R14.Pin_0, R15.Pin_1, J2.pin2
  N26: J1.pin4, R10.Pin_0, R11.Pin_1, J2.pin4
  N27: J1.pin5, R8.Pin_0, R9.Pin_1
  N28: J1.pin7, R12.Pin_0, R13.Pin_1
  N29: R13.Pin_0, R15.Pin_0

notes:
  13 - SCK
  12 - MISO
  11 - MOSI
  Reproductor MP3 con Arduino, (c) Jose Daniel Herrera. Arduino Guay                    http://arduino-guay.blogspot.com
  Módulo MP3
  3,3 V
  CLK
  MISO
  MOSI
  DCS
  CS
  RESET
  DREQ
  GND
  Tarjeta SD
  3,3 V
  CLK
  MISO
  MOSI
  CS
  GND
  Ver sólo el apartado esquema
  See only Schematic
