# Fritzing sketch id3377_snake_with_IR (saved by Fritzing 0.9.2b)
breadboards: 1

parts:
  U1 = DISPLAY NOKIA 5110
  Part2 = Arduino Nano (Rev3.0) (ICSP)
  VCC1 = Battery
  IR3 = prefix0000

nets (from the breadboard view):
  N1: U1.connector0, Part2.D3
  N2: U1.connector1, Part2.D4
  N3: U1.connector2, Part2.D5
  N4: U1.connector3, Part2.D6
  N5: U1.connector4, Part2.D7
  N6: U1.connector5, U1.connector7, Part2.GND, VCC1.+, IR3.connector2
  N7: U1.connector8, Part2.5V, VCC1.-, IR3.connector1
  N8: Part2.D11/MOSI, IR3.connector0
