# Fritzing sketch id337_Annoy_A_Troy_0 (saved by Fritzing 0.8.5b)
circuit board: 5.39636cm x 4.92894cm
breadboards: 1

parts:
  C1 = Electrolytic Capacitor [capacitance=1µF package="100 mil [THT, electrolytic]"]
  U1 = Voltage Regulator - 5V [package="TO220 [THT]"]
  J1 = Piezo Speaker
  U2 = attiny85 [package=dip]
  Q1 = NPN-Transistor [package="TO92 [THT]"]
  S1 = Pushbutton [package="[SMD]"]
  LED1 = LED - 5mm [color="Red (633nm)" package="5 mm [THT]"]
  LED2 = LED - 5mm [color="Red (633nm)" package="5 mm [THT]"]
  VCC1 = Battery block 9V
  R1 = 2000ohmRes
  R2 = 2000ohmRes
  C2 = cap100uf

nets (from the pcb view):
  N1: C1.-, U1.GND, J1.pin1, S1.Pin_3, S1.Pin_4, VCC1.-, R1.connector1, R2.connector0, C2.connector0
  N2: C1.+, U1.input_voltage, VCC1.+
  N3: U1.output_voltage, U2.Pin_8, Q1.C, LED1.anode, C2.connector1
  N4: J1.pin2, Q1.E, LED2.anode
  N5: U2.Pin_1, S1.Pin_1, S1.Pin_2
  N6: U2.Pin_2, Q1.B
  N7: LED1.cathode, R2.connector1
  N8: LED2.cathode, R1.connector0
