# Fritzing sketch id3381_Resin_printer_0 (saved by Fritzing 0.9.2b)
breadboards: 1

parts:
  Part1 = Logic Level Converter
  Part2 = Logic Level Converter
  JP1 = Header 3 [package=molex-1x3_lock]
  JP2 = Header 3 [package=molex-1x3_lock]
  JP5 = Header 10 [package=1x10-2mm-smd]
  JP6 = Header 8 [package=1x08_smd_alt]
  Q1 = Basic FET P-Channel [package="TO220 [THT]"]
  JP3 = Header 2 [package=screwterminal-3.5mm-2_lock]
  JP7 = Header 2 [package=screwterminal-3.5mm-2_lock]
  JP8 = Header 1 [package=smtso-256-et]
  JP9 = Header 1 [package=smtso-256-et]
  R1 = Resistor [tolerance=±5% resistance=220 package=THT]

nets:
  N1: Part1.TX2_LV, JP5.4
  N2: Part1.RX2_LV, JP5.3
  GND: Part1.GND, Part2.GND, JP1.2, JP5.10, Q1.source, JP3.1
  N3: Part1.LV, Part2.LV, JP1.3
  N4: Part1.RX_LV, JP5.2
  N5: Part1.TX_LV, JP5.1
  N6: Part1.TX_HV, JP6.1
  N7: Part1.RX_HV, JP6.2
  N8: Part1.HV, Part2.HV, JP1.1, JP2.2, R1.Pin_0
  N9: Part1.RX2_HV, JP6.3
  N10: Part1.TX2_HV, JP6.4
  N11: Part2.TX2_LV, JP5.8
  N12: Part2.RX2_LV, JP5.7
  N13: Part2.RX_LV, JP5.6
  N14: Part2.TX_LV, JP5.5
  N15: Part2.TX_HV, JP6.5
  N16: Part2.RX_HV, JP6.6
  N17: Part2.RX2_HV, JP6.7
  N18: Part2.TX2_HV, JP6.8
  N19: JP2.1, R1.Pin_1
  N20: JP2.3, JP9.1
  N21: Q1.gate, JP8.1
  N22: Q1.drain, JP7.1
  N23: JP3.2, JP7.2
