# Fritzing sketch id3382_Resistance.Touch.Circuit..v.2014.11.13.n01_0 (saved by Fritzing 0.9.0b)
circuit board: 8.46667cm x 5.64444cm
breadboards: 1

parts:
  Q1 = NPN-Transistor [package="TO92 [THT]"]
  Q2 = NPN-Transistor [package="TO92 [THT]"]
  VCC1 = Battery block 9V
  LED1 = LED - 5mm [color="Red (633nm)" package="5 mm [THT]"]
  R1 = Resistor [tolerance=±1% resistance=1k package=THT]
  R2 = Resistor [tolerance=±1% resistance=1k package=THT]

nets:
  N1: Q1.E, Q2.E, LED1.anode
  N2: Q1.B, R1.Pin_1
  N3: Q1.C, Q2.B
  N4: Q2.C, VCC1.-
  N5: VCC1.+, R2.Pin_0
