# Fritzing sketch id3383_handheldgame_0 (saved by Fritzing 0.9.2b)
breadboards: 2

parts:
  Part2 = Arduino Uno (Rev3)
  R1 = Resistor [tolerance=±5% resistance=10k package=THT]
  R2 = Resistor [tolerance=±5% resistance=10k package=THT]
  R3 = Resistor [tolerance=±5% resistance=10k package=THT]
  R4 = Resistor [tolerance=±5% resistance=10k package=THT]
  R5 = Resistor [tolerance=±5% resistance=1k package=THT]
  S1 = Pushbutton [package="[THT]"]
  S2 = Pushbutton [package="[THT]"]
  R6 = Resistor [tolerance=±5% resistance=10k package=THT]
  R7 = Resistor [tolerance=±5% resistance=10k package=THT]

nets:
  N1: Part2.D11_PWM/MOSI, S2.Pin_1, S2.Pin_2, R6.Pin_0
  N2: Part2.D12/MISO, S1.Pin_1, S1.Pin_2, R7.Pin_0
  N3: Part2.GND, R6.Pin_1, R7.Pin_1
  N4: Part2.D3_PWM, R4.Pin_0
  N5: Part2.D4, R3.Pin_0
  N6: Part2.D5_PWM, R2.Pin_0
  N7: Part2.D6_PWM, R1.Pin_0
  N8: Part2.D7, R5.Pin_0
  N9: Part2.3V3, S1.Pin_3, S1.Pin_4, S2.Pin_3, S2.Pin_4
