# Fritzing sketch id3384_REVEILLE_AFFICHEUR_LCD_0 (saved by Fritzing 0.8.5b)
breadboards: 1

parts:
  LCD1 = LCD screen
  Composants1 = Arduino Uno (Rev3)
  RTC1 = PCF8564_RTC_Breakout
  R1 = Trimmer Potentiometer [maximum_resistance=10kΩ package=THT]
  R2 = Resistor [tolerance=±5% resistance=10k package=THT]
  R3 = Resistor [tolerance=±5% resistance=10k package=THT]
  S1 = Pushbutton [package="[THT]"]
  S2 = Pushbutton [package="[THT]"]
  S3 = Pushbutton [package="[THT]"]
  R4 = Resistor [tolerance=±5% resistance=10k package=THT]
  R5 = Resistor [tolerance=±5% resistance=10k package=THT]
  R6 = Resistor [tolerance=±5% resistance=10k package=THT]

nets:
  VSS: LCD1.VSS, LCD1.R/W, LCD1.LED+, LCD1.LED-, Composants1.GND, RTC1.connector2, R1.leg2, R4.Pin_1, R5.Pin_1, R6.Pin_1
  VDD: LCD1.VDD, Composants1.5V, RTC1.connector1, R1.leg1, R2.Pin_1, R3.Pin_1, S1.Pin_3, S1.Pin_4, S2.Pin_3, S2.Pin_4, S3.Pin_3, S3.Pin_4
  N1: LCD1.V0, R1.wiper
  N2: LCD1.RS, Composants1.D2
  N3: LCD1.E, Composants1.D3_PWM
  N4: LCD1.DB4, Composants1.D4
  N5: LCD1.DB5, Composants1.D5_PWM
  N6: LCD1.DB6, Composants1.D6_PWM
  N7: LCD1.DB7, Composants1.D7
  N8: Composants1.A4/SDA, RTC1.connector3, R3.Pin_0
  N9: Composants1.A5/SCL, RTC1.connector4, R2.Pin_0
  N10: Composants1.D10_PWM/SS, S2.Pin_1, S2.Pin_2, R4.Pin_0
  N11: Composants1.D11_PWM/MOSI, S1.Pin_1, S1.Pin_2, R5.Pin_0
  N12: Composants1.D12/MISO, S3.Pin_1, S3.Pin_2, R6.Pin_0

notes:
  PLUS
  MOINS
  SET
