# Fritzing sketch id3385_ReverseDC_0 (saved by Fritzing 0.8.0b)
breadboards: 1

parts:
  Q1 = NPN-Transistor [package="TO92 [THT]"]
  Q2 = NPN-Transistor [package="TO92 [THT]"]
  Q3 = NPN-Transistor [package="TO92 [THT]"]
  Q4 = NPN-Transistor [package="TO92 [THT]"]
  Componente1 = Arduino Mega 2560 (Rev3)
  M1 = DC Motor
  D1 = Rectifier Diode [part_number=1N4001 package="300 mil [THT]"]

nets:
  N1: Q1.E, Q3.E, D1.cathode
  N2: Q1.B, Componente1.D9_PWM
  N3: Q1.C, Q4.E, M1.pin_1
  N4: Q2.E, Q3.C, M1.pin_2
  N5: Q2.B, Componente1.D8_PWM
  N6: Q2.C, Q4.C, Componente1.GND
  N7: Q3.B, Componente1.D7_PWM
  N8: Q4.B, Componente1.D6_PWM
  N9: Componente1.3V3, D1.anode

notes:
  // This code uses 4 NPN transistors to reverse the direction of a DC Motor without using Relays or Motor Driver ICs.
  // I'm sorry if you burn your Arduino/Pins with this code/circuit, I'm not really sure of how secure it is. Maybe adding a diode to each digital pin, avoiding reverse current for some reason?
  // I'm just starting with Arduino and Electronics and felt bad about having to buy more components that I didn't have just to do this.
  // You are much likely able to do this with a much simpler circuit. Please show me how dumb I am, send me an e-mail with your idea: caulitomaz@gmail.com
  // @author Cauli Tomaz, http://www.facebook.com/caulitomaz
  int antiSwitchP = 8; // Counter-clockwise transistor, +V
  int antiSwitchN = 9; // Counter-clockwise transistor, GND
  int cwSwitchP = 7; // Clockwise transistor, +V
  int cwSwitchN = 6; // Clockwise transistor, GND
  void setup() {
  // We are using those pins as OUTPUT, since we are setting it to HIGH to "switch on" a transistor and LOW to "switch it off"
  pinMode(antiSwitchP, OUTPUT);
  pinMode(antiSwitchN, OUTPUT);
  pinMode(cwSwitchP, OUTPUT);
  pinMode(cwSwitchN, OUTPUT);
  }
  void loop(){
  digitalWrite(cwSwitchP, LOW); // guarantee initial state
  digitalWrite(cwSwitchN, LOW); // guarantee initial state
  // Now lets turn the Motor counter-clockwise
  digitalWrite(antiSwitchP, HIGH);
  digitalWrite(antiSwitchN, HIGH);
  delay(1000);
  // Turn it off
  digitalWrite(antiSwitchP, LOW);
  digitalWrite(antiSwitchN, LOW);
  delay(1000);
  // Now lets turn the Motor clockwise
  digitalWrite(cwSwitchP, HIGH);
  digitalWrite(cwSwitchN, HIGH);
  delay(1000);
  // Turn it off
  digitalWrite(cwSwitchP, LOW);
  digitalWrite(cwSwitchN, LOW);
  delay(1000);
  }
