# Fritzing sketch id3386_arduino_watermelon_0 (saved by Fritzing 0.9.3b)
circuit board: 8.46667cm x 5.64444cm

parts:
  Piezo_buzzer = Piezo Speaker
  R1 = Resistor [tolerance=±5% resistance=1M package=THT]
  Part1 = Arduino Uno (Rev3) - ICSP

nets:
  N1: Piezo_buzzer.pin1, R1.Pin_0, Part1.GND
  N2: Piezo_buzzer.pin2, R1.Pin_1, Part1.A0
