# Fritzing sketch id3387_sketch_0 (saved by Fritzing 0.9.2b)

parts:
  Arduino_UNO = Arduino Uno (Rev3)
  Arduino_Nano = Arduino Nano (Rev3.0)
  Tx = mystery part, 3 pins [chip_label=?]
  Rx = mystery part, 4 pins [chip_label=?]

nets:
  N1: Arduino_UNO.D12/MISO, Tx.pin1
  N2: Arduino_UNO.GND, Tx.pin3
  N3: Arduino_UNO.5V, Tx.pin2
  N4: Arduino_Nano.D11/MOSI, Rx.pin3
  N5: Arduino_Nano.GND, Rx.pin4
  N6: Arduino_Nano.5V, Rx.pin1

notes:
  Transmitter
  Reciever
