# Fritzing sketch id338_migavac555_0 (saved by Fritzing 0.7.10b)
breadboards: 1

parts:
  IC1 = IC, DIP package, 8 pins [chip_label=NE555]
  C1 = Tantalum Capacitor [capacitance="1 μF" package="100 mil [THT, tantalum]"]
  C2 = Ceramic Capacitor [capacitance=100nF package="100 mil [THT, multilayer]"]
  R1 = Resistor [tolerance=±5% resistance=330 package=THT]
  LED1 = LED - 5mm [color="Red (633nm)" package="5 mm [THT]"]
  R2 = Resistor [tolerance=±5% resistance=47k package=THT]
  R3 = Trimmer Potentiometer [maximum_resistance=1MΩ package=THT]
  VCC1 = 4 x AAA Battery Mount

nets (from the breadboard view):
  N1: IC1.pin1, C1.-, C2.0, LED1.cathode, VCC1.-
  N2: IC1.pin2, IC1.pin6, C1.+, R2.Pin_1
  N3: IC1.pin3, R1.Pin_0
  N4: IC1.pin4, IC1.pin8, R3.wiper
  N5: IC1.pin5, C2.1
  N6: IC1.pin7, R2.Pin_0, R3.leg2
  N7: R1.Pin_1, LED1.anode
  N8: R3.leg1, VCC1.+
