# Fritzing sketch id3390_RGBWithoutArduinoWithPotentiometers_0 (saved by Fritzing 0.9.0b)
breadboards: 1

parts:
  LED1 = RGB LED (com. cathode, rgb) [package="5 mm [THT]"]
  R1 = TRIMPOT [package=3386u]
  R2 = TRIMPOT [package=3386u]
  R3 = TRIMPOT [package=3386u]
  R4 = Resistor [tolerance=±5% resistance=220 package="1206 [SMD]"]
  R5 = Resistor [tolerance=±5% resistance=220 package="1206 [SMD]"]
  R6 = Resistor [tolerance=±5% resistance=220 package="1206 [SMD]"]

nets:
  N1: LED1.red_anode, R4.Pin_1
  N2: LED1.common_cathode, R1.CCW, R2.CCW, R3.CCW
  N3: LED1.green_anode, R5.Pin_1
  N4: LED1.blue_anode, R6.Pin_0
  N5: R1.WIPER, R4.Pin_0
  N6: R1.CW, R2.CW, R3.CW
  N7: R2.WIPER, R5.Pin_0
  N8: R3.WIPER, R6.Pin_1

notes:
  VDD (5V)
  GND
  Potentiometers: 10K
  Resistors: 220 Ohms
  Without Arduino
