# Fritzing sketch id3391_RFId_7Display_0 (saved by Fritzing 0.7.12b)
breadboards: 1

parts:
  Arduino1 = Arduino
  7_Segment1 = 7-Segment LED Display [package=THT]
  R1 = Resistor [tolerance=±5% resistance=220 package=THT]
  R2 = Resistor [tolerance=±5% resistance=220 package=THT]
  R3 = Resistor [tolerance=±5% resistance=220 package=THT]
  R4 = Resistor [tolerance=±5% resistance=220 package=THT]
  R5 = Resistor [tolerance=±5% resistance=220 package=THT]
  R6 = Resistor [tolerance=±5% resistance=220 package=THT]
  R7 = Resistor [tolerance=±5% resistance=220 package=THT]
  RC523 = rc522

nets:
  N1: Arduino1.D13, RC523.connector10
  N2: Arduino1.D12, RC523.connector12
  N3: Arduino1.D11, RC523.connector11
  N4: Arduino1.D10, RC523.connector9
  N5: Arduino1.D9, RC523.connector14
  N6: Arduino1.D8, R3.Pin_1
  N7: Arduino1.D7, R5.Pin_1
  N8: Arduino1.D6, R4.Pin_1
  N9: Arduino1.D5, R7.Pin_1
  N10: Arduino1.D4, R1.Pin_1
  N11: Arduino1.D3, R2.Pin_1
  N12: Arduino1.D2, R6.Pin_1
  N13: Arduino1.3V3, RC523.connector15
  N14: Arduino1.GND, 7_Segment1.commAnode#7
  N15: 7_Segment1.cathodeE, R4.Pin_0
  N16: 7_Segment1.cathodeD, R5.Pin_0
  N17: 7_Segment1.cathodeC, R3.Pin_0
  N18: 7_Segment1.cathodeB, R7.Pin_0
  N19: 7_Segment1.cathodeA, R1.Pin_0
  N20: 7_Segment1.cathodeF, R2.Pin_0
  N21: 7_Segment1.cathodeG, R6.Pin_0
