# Fritzing sketch id3392_rfid_rc522_0 (saved by Fritzing 0.9.3b)
breadboards: 1

parts:
  LCD1 = LCD screen
  Componente2 = Arduino Mega 2560 (Rev3)
  R1 = Rotary Potentiometer (Small) [maximum_resistance=100kΩ package=THT]

nets:
  N1: LCD1.VSS, LCD1.R/W, LCD1.LED-, R1.leg1
  N2: LCD1.VDD, LCD1.LED+
  N3: LCD1.V0, R1.wiper
  N4: LCD1.RS, Componente2.D12_PWM
  N5: LCD1.E, Componente2.D11_PWM
  N6: LCD1.DB4, Componente2.D5_PWM
  N7: LCD1.DB5, Componente2.D4_PWM
  N8: LCD1.DB6, Componente2.D3_PWM
  N9: LCD1.DB7, Componente2.D2_PWM
