# Fritzing sketch id3393_Untitled_Sketch_2_0 (saved by Fritzing 0.9.2b)
breadboards: 1

parts:
  Eleman1 = Arduino Uno (Rev3)
  P1 = S1133 Si Photodiode [package="8mm Ceramic [THT]"]
  P2 = S1133 Si Photodiode [package="8mm Ceramic [THT]"]
  Q1 = LTR-301 [package=ltr-301]
  Q2 = LTR-301 [package=ltr-301]
  J1 = Basic Servo
  R1 = Resistor [tolerance=±5% resistance=220 package=THT]
  R2 = Resistor [tolerance=±5% resistance=220 package=THT]
  R3 = Resistor [tolerance=±5% resistance=220 package=THT]
  R4 = Resistor [tolerance=±5% resistance=220 package=THT]
  Eleman2 = RFID USB Reader

nets:
  N1: Eleman1.A0, Q1.C, R4.Pin_0
  N2: Eleman1.A1, Q2.E, R3.Pin_1
  N3: Eleman1.D9_PWM, J1.pulse
  N4: Eleman1.D10_PWM/SS, Eleman2.ANT1
  N5: Eleman1.D11_PWM/MOSI, Eleman2.CP
  N6: Eleman1.D12/MISO, Eleman2.ANT2
  N7: Eleman1.D13/SCK, Eleman2.GNDT
  GND: Eleman1.GND, P1.cathode, Q1.E, Q2.C, J1.gnd, Eleman2.GND
  N8: Eleman1.D0/RX, R3.Pin_0
  N9: Eleman1.D1/TX, R4.Pin_1
  N10: Eleman1.D3_PWM, R1.Pin_0
  N11: Eleman1.D4, R2.Pin_1
  N12: Eleman1.D5_PWM, Eleman2.TX-O
  3V3: Eleman1.3V3, Eleman2.VCC
  5V: Eleman1.5V, J1.vcc
  N13: P1.anode, R2.Pin_0
  N14: P2.cathode, R1.Pin_1
