# Fritzing sketch id3394_simplificado_0 (saved by Fritzing 0.9.2b)
perfboards: 1

parts:
  U1 = ESP8266_module [part_number=ESP8266]
  Componente1 = Arduino Pro Mini v13
  Componente2 = RFID-RC522
  YF-S201_Flow_Meter1 = prefix0000_RichardBruneau
  R1 = Resistor [tolerance=±5% resistance=220 package=THT]
  R2 = Resistor [tolerance=±5% resistance=220 package=THT]
  R3 = Resistor [tolerance=±5% resistance=10k package=THT]
  R4 = Resistor [tolerance=±5% resistance=220 package=THT]
  KY-1 = keyes
  U2 = V_REG_LD1117VXX [package=78xxl]
  Power_plug1 = Power plug
  C1 = Capacitor Polarized [package=cpol-radial-100uf-25v]
  C2 = Capacitor Polarized [package=cpol-radial-100uf-25v]
  J1 = male pin header, 4 pins [form="♂ (male)"]
  J4 = male pin header, 5 pins [form="♂ (male)"]
  LED2 = LED - 3mm [color="Red (633nm)" package="3 mm [THT]"]
  J7 = male pin header, 1 pin [form="♂ (male)"]  # not connected
  J8 = male pin header, 1 pin [form="♂ (male)"]
  J2 = male pin header, 1 pin [form="♂ (male)"]
  J9 = male pin header, 1 pin [form="♂ (male)"]
  J10 = male pin header, 3 pins [form="♂ (male)"]
  J11 = male pin header, 3 pins [form="♂ (male)"]
  J12 = male pin header, 3 pins [form="♂ (male)"]
  J5 = male pin header, 5 pins [form="♂ (male)"]
  J13 = male pin header, 1 pin [form="♂ (male)"]
  red_=_3v3 = male pin header, 8 pins [form="♂ (male)"]
  J6 = male pin header, 1 pin [form="♂ (male)"]
  J14 = male pin header, 1 pin [form="♂ (male)"]  # not connected

nets:
  N1: U1.connector0, J5.pin1
  N2: U1.connector1, J5.pin2
  N3: U1.connector5, J5.pin3
  N4: U1.connector6, J5.pin4
  N5: U1.connector7, J5.pin5
  N6: Componente1.GND, R1.Pin_0, C1.+, J4.pin4, J8.pin1, J11.pin2
  N7: Componente1.VCC, U2.IN
  N8: Componente1.D13/SCK, J1.pin1
  N9: Componente1.D12/MISO, J1.pin2
  N10: Componente1.D11_PWM/MOSI, J1.pin3
  N11: Componente1.D10_PWM/SS, J1.pin4
  N12: Componente1.D7, J2.pin1
  N13: Componente1.D6_PWM, J9.pin1
  N14: Componente1.D4, R4.Pin_1
  N15: Componente1.D2, J11.pin3
  N16: Componente1.D1/RX, J4.pin5
  N17: Componente1.D0/TX, R2.Pin_1
  N18: Componente2.connector8, red_=_3v3.pin8
  N19: Componente2.connector9, red_=_3v3.pin7
  N20: Componente2.connector10, red_=_3v3.pin6
  N21: Componente2.connector11, red_=_3v3.pin5
  N22: Componente2.connector13, LED2.cathode
  N23: Componente2.connector14, red_=_3v3.pin2
  N24: Componente2.connector15, red_=_3v3.pin1
  N25: YF-S201_Flow_Meter1.connector0, J12.pin3
  N26: YF-S201_Flow_Meter1.connector1, J12.pin2
  N27: YF-S201_Flow_Meter1.connector2, J12.pin1
  N28: R1.Pin_1, R2.Pin_0, J4.pin1
  N29: R3.Pin_0, J4.pin2
  N30: R3.Pin_1, J4.pin3
  N31: R4.Pin_0, J13.pin1
  N32: KY-1.connector0, J10.pin1
  N33: KY-1.connector1, J10.pin2
  N34: KY-1.connector2, J10.pin3
  GND: U2.GND, Power_plug1.GND
  N35: Power_plug1.VCC, C1.-, J11.pin1
  N36: C2.+, J6.pin1
  N37: LED2.anode, red_=_3v3.pin4

notes:
  fios soldados no leitor rfid, led e esp8266 com pelo menos 40 cm
  fios de conexão o módulo de rele, será curto, entre 10 a 20cm.
