# Fritzing sketch id3395_rfidservo_0 (saved by Fritzing 0.9.2b)
circuit board: 10.775cm x 6.67568cm
breadboards: 1

parts:
  Eleman1 = RFID-RC522  # not connected
  Eleman2 = Arduino Uno (Rev3)
  J1 = Basic Servo
  LED1 = RGB LED (com. anode, rbg) [package="5 mm [THT]"]
  R2 = Resistor [tolerance=±5% resistance=220 package="0805 [SMD]"]
  R3 = Resistor [tolerance=±5% resistance=220 package="0805 [SMD]"]
  R4 = Resistor [tolerance=±5% resistance=220 package="0805 [SMD]"]

nets:
  N1: Eleman2.D3_PWM, J1.pulse
  N2: Eleman2.D5_PWM, R4.Pin_0
  5V: Eleman2.5V, J1.vcc
  N3: J1.gnd, LED1.green_cathode
  N4: LED1.red_cathode, R2.Pin_1
  N5: LED1.common_anode, R3.Pin_1
  N6: LED1.blue_cathode, R4.Pin_1
