# Fritzing sketch id3396_RFID_0 (saved by Fritzing 0.8.7b)
circuit board: 5.44952cm x 4.35036cm
breadboards: 1

parts:
  U4 = attiny85 [package=dip]
  J1 = Piezo Speaker
  J3 = Power Jack [package=power_jack_slot]
  RFID1 = RFID Reader
  R1 = Resistor [tolerance=±5% resistance=220 package=THT]
  S1 = Pushbutton [package="[THT]"]
  U2 = XBEE-1 [package=xbee-1]

nets (from the pcb view):
  N1: U4.Pin_1, S1.Pin_3, S1.Pin_4
  N2: U4.Pin_2, RFID1.D0, U2.DOUT
  N3: U4.Pin_3, U2.DIN
  N4: U4.Pin_4, R1.Pin_0, U2.DTR
  +5V: U4.Pin_8, J1.pin2, J3.PWR, RFID1.+5V, S1.Pin_1, S1.Pin_2, U2.VDD
  N5: J1.pin1, RFID1.LED
  N6: J3.GND, R1.Pin_1
  GND: RFID1.GND, U2.GND

notes:
  TX RX
