# Fritzing sketch id3397_rfid_lcd_test_0 (saved by Fritzing 0.9.2b)
breadboards: 1

parts:
  LED1 = smd LED [color="Red (633nm)" package="1206 [SMD]"]
  Part1 = Arduino Uno (Rev3)
  IIC2 = iic_converter
  LCD2 = LCD screen
  R1 = Resistor [tolerance=±5% resistance=220 package=THT]
  LED2 = smd LED [color="Green (565nm)" package="0805 [SMD]"]
  R2 = Resistor [tolerance=±5% resistance=220 package=THT]

nets:
  N1: LED1.cathode, Part1.GND, IIC2.connector16, LED2.cathode
  N2: LED1.anode, R2.Pin_0
  N3: Part1.A4/SDA, IIC2.connector18
  N4: Part1.A5/SCL, IIC2.connector19
  N5: Part1.5V, IIC2.connector17
  N6: IIC2.connector0, LCD2.VSS
  N7: IIC2.connector1, LCD2.VDD
  N8: IIC2.connector2, LCD2.V0
  N9: IIC2.connector3, LCD2.RS
  N10: IIC2.connector4, LCD2.R/W
  N11: IIC2.connector5, LCD2.E
  N12: IIC2.connector6, LCD2.DB0
  N13: IIC2.connector7, LCD2.DB1
  N14: IIC2.connector8, LCD2.DB2
  N15: IIC2.connector9, LCD2.DB3
  N16: IIC2.connector10, LCD2.DB4
  N17: IIC2.connector11, LCD2.DB5
  N18: IIC2.connector12, LCD2.DB6
  N19: IIC2.connector13, LCD2.DB7
  N20: IIC2.connector14, LCD2.LED+
  N21: IIC2.connector15, LCD2.LED-
  N22: IIC2.connector20, IIC2.connector21
  N23: R1.Pin_0, LED2.anode
