# Fritzing sketch id3398_EB5222d_0 (saved by Fritzing 0.9.2b)
circuit board: 10.775cm x 6.67568cm
breadboards: 1

parts:
  Eleman1 = Arduino Pro Mini v13
  R1 = Resistor [tolerance=±5% resistance=220 package=THT]
  4x4_Keypad = male pin header, 8 pins [form="♂ (male)"]
  RC522 = male pin header, 8 pins [form="♂ (male)"]
  LCD_5110 = male pin header, 8 pins [form="♂ (male)"]
  Q1 = NPN-Transistor [package="TO92 [THT]"]
  R10 = Resistor [tolerance=±5% resistance=220 package=THT]
  SPKR1 = Loudspeaker  # not connected
  LED1 = LED - 5mm [color="Red (633nm)" package="5 mm [THT]"]  # not connected
  Keypad4x1 = Keypad4x4
  3v3_Input = male pin header, 2 pins [form="♂ (male)"]
  5V_Input = male pin header, 2 pins [form="♂ (male)"]
  LED_G = male pin header, 2 pins [form="♂ (male)"]
  Buzzer = male pin header, 2 pins [form="♂ (male)"]
  LED_R = male pin header, 2 pins [form="♂ (male)"]
  R11 = Resistor [tolerance=±5% resistance=220 package=THT]
  Q2 = NPN-Transistor [package="TO92 [THT]"]
  Q3 = NPN-Transistor [package="TO92 [THT]"]
  LED2 = LED - 5mm [color="Green (555nm)" package="5 mm [THT]"]  # not connected
  R12 = Resistor [tolerance=±5% resistance=220 package=THT]
  R13 = Resistor [tolerance=±5% resistance=220 package=THT]
  R14 = Resistor [tolerance=±5% resistance=220 package=THT]
  U1 = PCF8574 [package="DIP16 [THT]"]

nets:
  GND: Eleman1.GND, RC522.pin6, LCD_5110.pin2, Q1.E, 5V_Input.pin1, Q2.E, Q3.E, U1.GND
  N1: Eleman1.A5, U1.SDA
  N2: Eleman1.RAW, LCD_5110.pin8, 5V_Input.pin2, R12.Pin_1, R13.Pin_1, R14.Pin_1, U1.VCC
  N3: Eleman1.A3, U1.SCL
  N4: Eleman1.D13/SCK, RC522.pin2, LCD_5110.pin7
  N5: Eleman1.D12/MISO, RC522.pin4
  N6: Eleman1.D11_PWM/MOSI, RC522.pin3, LCD_5110.pin6
  N7: Eleman1.D10_PWM/SS, RC522.pin1
  N8: Eleman1.D9_PWM, RC522.pin7
  N9: Eleman1.D8, R11.Pin_1
  N10: Eleman1.D7, R10.Pin_1
  N11: Eleman1.D6_PWM, R1.Pin_1
  N12: Eleman1.D5_PWM, LCD_5110.pin5
  N13: Eleman1.D4, LCD_5110.pin3
  N14: Eleman1.D3_PWM, LCD_5110.pin4
  N15: R1.Pin_0, Q1.B
  N16: 4x4_Keypad.pin1, U1.P0
  N17: 4x4_Keypad.pin2, U1.P1
  N18: 4x4_Keypad.pin3, U1.P2
  N19: 4x4_Keypad.pin4, U1.P3
  N20: 4x4_Keypad.pin5, U1.P4
  N21: 4x4_Keypad.pin6, U1.P5
  N22: 4x4_Keypad.pin7, U1.P6
  N23: 4x4_Keypad.pin8, U1.P7
  N24: RC522.pin8, LCD_5110.pin1, 3v3_Input.pin1
  N25: Q1.C, Buzzer.pin1
  N26: R10.Pin_0, Q2.B
  N27: Keypad4x1.connector0, Keypad4x1.connector1, Keypad4x1.connector2, Keypad4x1.connector4, Keypad4x1.connector6, Keypad4x1.connector7, Keypad4x1.connector8
  N28: LED_G.pin1, Q2.C
  N29: LED_G.pin2, R12.Pin_0
  N30: Buzzer.pin2, R14.Pin_0
  N31: LED_R.pin1, Q3.C
  N32: LED_R.pin2, R13.Pin_0
  N33: R11.Pin_0, Q3.B
