# Fritzing sketch id3399_RaspberryPI_RFID_RC522_0 (saved by Fritzing 0.9.3b)
circuit board: 8.46667cm x 5.64444cm

parts:
  Raspberry_Pi_1 = Raspberry Pi 3 [part_number=RPI-3-V1.2]
  MFRC523 = RFID-RC522

nets:
  3V3: Raspberry_Pi_1.3v3, Raspberry_Pi_1.3V3, MFRC523.connector8
  N1: Raspberry_Pi_1.GPIO10, MFRC523.connector13
  N2: Raspberry_Pi_1.GPIO9, MFRC523.connector12
  N3: Raspberry_Pi_1.GPIO11, MFRC523.connector14
  N4: Raspberry_Pi_1.GPIO8, MFRC523.connector15
  N5: Raspberry_Pi_1.GPIO25, MFRC523.connector9
  N6: Raspberry_Pi_1.GND, MFRC523.connector10
  N7: Raspberry_Pi_1.GPIO24, MFRC523.connector11
