# Fritzing sketch id3400_RFID_Reader__0 (saved by Fritzing 0.3.10b)
breadboards: 1

parts:
  Arduino1 = Arduino
  S1 = Pushbutton [package="[THT]"]
  R1 = Resistor [resistance=10k package=THT]
  J2 = female pin header, 4 pins
  R2 = Resistor [resistance=220 package=THT]
  R3 = Resistor [resistance=10k package=THT]
  J4 = female pin header, 5 pins

nets:
  N1: Arduino1.GND, R1.Pin_1, J2.pin4, R3.Pin_1, J4.pin3
  N2: Arduino1.D8, R1.Pin_0
  N3: Arduino1.D2, R2.Pin_1
  N4: Arduino1.D1TX, J4.pin1, J4.pin5
  N5: Arduino1.D0RX, J2.pin3
  N6: Arduino1.+5V, S1.Pin_1, S1.Pin_2, J2.pin1, J4.pin2, J4.pin4
  N7: J2.pin2, R2.Pin_0, R3.Pin_0

notes:
  Simple RFID Reader
  2009 - hairmare@purplehaze.ch
