# Fritzing sketch id3401_PCB_for_plinth___64_leds_0 (saved by Fritzing 0.7.12b)

parts:
  LED1 = RGB LED (com. cathode, rgb) [package="5 mm [THT]"]
  LED2 = RGB LED (com. cathode, rgb) [package="5 mm [THT]"]
  LED3 = RGB LED (com. cathode, rgb) [package="5 mm [THT]"]
  LED4 = RGB LED (com. cathode, rgb) [package="5 mm [THT]"]
  LED5 = RGB LED (com. cathode, rgb) [package="5 mm [THT]"]
  LED6 = RGB LED (com. cathode, rgb) [package="5 mm [THT]"]
  LED7 = RGB LED (com. cathode, rgb) [package="5 mm [THT]"]
  LED8 = RGB LED (com. cathode, rgb) [package="5 mm [THT]"]
  LED9 = RGB LED (com. cathode, rgb) [package="5 mm [THT]"]
  LED10 = RGB LED (com. cathode, rgb) [package="5 mm [THT]"]
  LED11 = RGB LED (com. cathode, rgb) [package="5 mm [THT]"]
  LED12 = RGB LED (com. cathode, rgb) [package="5 mm [THT]"]
  LED13 = RGB LED (com. cathode, rgb) [package="5 mm [THT]"]
  LED14 = RGB LED (com. cathode, rgb) [package="5 mm [THT]"]
  LED15 = RGB LED (com. cathode, rgb) [package="5 mm [THT]"]
  LED16 = RGB LED (com. cathode, rgb) [package="5 mm [THT]"]
  LED17 = RGB LED (com. cathode, rgb) [package="5 mm [THT]"]
  LED18 = RGB LED (com. cathode, rgb) [package="5 mm [THT]"]
  LED19 = RGB LED (com. cathode, rgb) [package="5 mm [THT]"]
  LED20 = RGB LED (com. cathode, rgb) [package="5 mm [THT]"]
  LED21 = RGB LED (com. cathode, rgb) [package="5 mm [THT]"]
  LED22 = RGB LED (com. cathode, rgb) [package="5 mm [THT]"]
  LED23 = RGB LED (com. cathode, rgb) [package="5 mm [THT]"]
  LED24 = RGB LED (com. cathode, rgb) [package="5 mm [THT]"]
  LED25 = RGB LED (com. cathode, rgb) [package="5 mm [THT]"]
  LED26 = RGB LED (com. cathode, rgb) [package="5 mm [THT]"]
  LED27 = RGB LED (com. cathode, rgb) [package="5 mm [THT]"]
  LED28 = RGB LED (com. cathode, rgb) [package="5 mm [THT]"]
  LED29 = RGB LED (com. cathode, rgb) [package="5 mm [THT]"]
  LED30 = RGB LED (com. cathode, rgb) [package="5 mm [THT]"]
  LED31 = RGB LED (com. cathode, rgb) [package="5 mm [THT]"]
  LED32 = RGB LED (com. cathode, rgb) [package="5 mm [THT]"]
  LED33 = RGB LED (com. cathode, rgb) [package="5 mm [THT]"]
  LED34 = RGB LED (com. cathode, rgb) [package="5 mm [THT]"]
  LED35 = RGB LED (com. cathode, rgb) [package="5 mm [THT]"]
  LED36 = RGB LED (com. cathode, rgb) [package="5 mm [THT]"]
  LED37 = RGB LED (com. cathode, rgb) [package="5 mm [THT]"]
  LED38 = RGB LED (com. cathode, rgb) [package="5 mm [THT]"]
  LED39 = RGB LED (com. cathode, rgb) [package="5 mm [THT]"]
  LED40 = RGB LED (com. cathode, rgb) [package="5 mm [THT]"]
  LED41 = RGB LED (com. cathode, rgb) [package="5 mm [THT]"]
  LED42 = RGB LED (com. cathode, rgb) [package="5 mm [THT]"]
  LED43 = RGB LED (com. cathode, rgb) [package="5 mm [THT]"]
  LED44 = RGB LED (com. cathode, rgb) [package="5 mm [THT]"]
  LED45 = RGB LED (com. cathode, rgb) [package="5 mm [THT]"]
  LED46 = RGB LED (com. cathode, rgb) [package="5 mm [THT]"]
  LED47 = RGB LED (com. cathode, rgb) [package="5 mm [THT]"]
  LED48 = RGB LED (com. cathode, rgb) [package="5 mm [THT]"]
  LED49 = RGB LED (com. cathode, rgb) [package="5 mm [THT]"]
  LED50 = RGB LED (com. cathode, rgb) [package="5 mm [THT]"]
  LED51 = RGB LED (com. cathode, rgb) [package="5 mm [THT]"]
  LED52 = RGB LED (com. cathode, rgb) [package="5 mm [THT]"]
  LED53 = RGB LED (com. cathode, rgb) [package="5 mm [THT]"]
  LED54 = RGB LED (com. cathode, rgb) [package="5 mm [THT]"]
  LED55 = RGB LED (com. cathode, rgb) [package="5 mm [THT]"]
  LED57 = RGB LED (com. cathode, rgb) [package="5 mm [THT]"]
  LED58 = RGB LED (com. cathode, rgb) [package="5 mm [THT]"]
  LED59 = RGB LED (com. cathode, rgb) [package="5 mm [THT]"]
  LED60 = RGB LED (com. cathode, rgb) [package="5 mm [THT]"]
  LED61 = RGB LED (com. cathode, rgb) [package="5 mm [THT]"]
  LED62 = RGB LED (com. cathode, rgb) [package="5 mm [THT]"]
  LED63 = RGB LED (com. cathode, rgb) [package="5 mm [THT]"]
  LED64 = RGB LED (com. cathode, rgb) [package="5 mm [THT]"]
  U1 = 74HC595 [package="DIP16 [THT]"]
  Arduino1 = Arduino
  U2 = 74HC595 [package="DIP16 [THT]"]
  U3 = 74HC595 [package="DIP16 [THT]"]
  U4 = 74HC595 [package="DIP16 [THT]"]
  LED56 = RGB LED (com. cathode, rgb) [package="5 mm [THT]"]

nets:
  N1: LED1.red_anode, LED2.red_anode, LED3.red_anode, LED4.red_anode, LED5.red_anode, LED6.red_anode, LED7.red_anode, LED8.red_anode, U2.Q7
  N2: LED1.common_cathode, LED9.common_cathode, LED17.common_cathode, LED25.common_cathode, LED33.common_cathode, LED41.common_cathode, LED49.common_cathode, LED57.common_cathode, U1.Q7
  N3: LED1.green_anode, LED9.green_anode, LED17.green_anode, LED25.green_anode, LED33.green_anode, LED41.green_anode, LED49.green_anode, LED57.green_anode, U4.Q7
  N4: LED1.blue_anode, LED9.blue_anode, LED17.blue_anode, LED25.blue_anode, LED33.blue_anode, LED41.blue_anode, LED49.blue_anode, LED57.blue_anode, U3.Q7
  N5: LED2.common_cathode, LED10.common_cathode, LED18.common_cathode, LED26.common_cathode, LED34.common_cathode, LED42.common_cathode, LED50.common_cathode, LED58.common_cathode, U1.Q6
  N6: LED2.green_anode, LED10.green_anode, LED18.green_anode, LED26.green_anode, LED34.green_anode, LED42.green_anode, LED50.green_anode, LED58.green_anode, U4.Q6
  N7: LED2.blue_anode, LED10.blue_anode, LED18.blue_anode, LED26.blue_anode, LED34.blue_anode, LED42.blue_anode, LED50.blue_anode, LED58.blue_anode, U3.Q6
  N8: LED3.common_cathode, LED11.common_cathode, LED19.common_cathode, LED27.common_cathode, LED35.common_cathode, LED43.common_cathode, LED51.common_cathode, LED59.common_cathode, U1.Q5
  N9: LED3.green_anode, LED11.green_anode, LED19.green_anode, LED27.green_anode, LED35.green_anode, LED43.green_anode, LED51.green_anode, LED59.green_anode, U4.Q5
  N10: LED3.blue_anode, LED11.blue_anode, LED19.blue_anode, LED27.blue_anode, LED35.blue_anode, LED43.blue_anode, LED51.blue_anode, LED59.blue_anode, U3.Q5
  N11: LED4.common_cathode, LED12.common_cathode, LED20.common_cathode, LED28.common_cathode, LED36.common_cathode, LED44.common_cathode, LED52.common_cathode, LED60.common_cathode, U1.Q4
  N12: LED4.green_anode, LED12.green_anode, LED20.green_anode, LED28.green_anode, LED36.green_anode, LED44.green_anode, LED52.green_anode, LED60.green_anode, U4.Q4
  N13: LED4.blue_anode, LED12.blue_anode, LED20.blue_anode, LED28.blue_anode, LED36.blue_anode, LED44.blue_anode, LED52.blue_anode, LED60.blue_anode, U3.Q4
  N14: LED5.common_cathode, LED13.common_cathode, LED21.common_cathode, LED29.common_cathode, LED37.common_cathode, LED45.common_cathode, LED53.common_cathode, LED61.common_cathode, U1.Q3
  N15: LED5.green_anode, LED13.green_anode, LED21.green_anode, LED29.green_anode, LED37.green_anode, LED45.green_anode, LED53.green_anode, LED61.green_anode, U4.Q3
  N16: LED5.blue_anode, LED13.blue_anode, LED21.blue_anode, LED37.blue_anode, LED45.blue_anode, LED53.blue_anode, LED61.blue_anode, U3.Q3
  N17: LED6.common_cathode, LED14.common_cathode, LED22.common_cathode, LED30.common_cathode, LED38.common_cathode, LED46.common_cathode, LED54.common_cathode, LED62.common_cathode, U1.Q2
  N18: LED6.green_anode, LED14.green_anode, LED22.green_anode, LED38.green_anode, LED46.green_anode, LED54.green_anode, LED62.green_anode, U4.Q2
  N19: LED6.blue_anode, LED14.blue_anode, LED22.blue_anode, LED30.blue_anode, LED38.blue_anode, LED46.blue_anode, LED54.blue_anode, LED62.blue_anode, U3.Q2
  N20: LED7.common_cathode, LED15.common_cathode, LED23.common_cathode, LED31.common_cathode, LED39.common_cathode, LED47.common_cathode, LED55.common_cathode, LED63.common_cathode, U1.Q1
  N21: LED7.green_anode, LED15.green_anode, LED23.green_anode, LED31.green_anode, LED39.green_anode, LED47.green_anode, LED55.green_anode, LED63.green_anode, U4.Q1
  N22: LED7.blue_anode, LED15.blue_anode, LED23.blue_anode, LED31.blue_anode, LED39.blue_anode, LED47.blue_anode, LED55.blue_anode, LED63.blue_anode, U3.Q1
  N23: LED8.common_cathode, LED16.common_cathode, LED24.common_cathode, LED32.common_cathode, LED40.common_cathode, LED48.common_cathode, LED64.common_cathode, U1.Q0, LED56.common_cathode
  N24: LED8.green_anode, LED16.green_anode, LED24.green_anode, LED32.green_anode, LED40.green_anode, LED48.green_anode, LED64.green_anode, U4.Q0, LED56.green_anode
  N25: LED8.blue_anode, LED16.blue_anode, LED24.blue_anode, LED32.blue_anode, LED40.blue_anode, LED48.blue_anode, LED64.blue_anode, U3.Q0, LED56.blue_anode
  N26: LED9.red_anode, LED10.red_anode, LED11.red_anode, LED12.red_anode, LED13.red_anode, LED14.red_anode, LED15.red_anode, LED16.red_anode, U2.Q6
  N27: LED17.red_anode, LED18.red_anode, LED19.red_anode, LED20.red_anode, LED21.red_anode, LED22.red_anode, LED23.red_anode, LED24.red_anode, U2.Q5
  N28: LED25.red_anode, LED26.red_anode, LED27.red_anode, LED28.red_anode, LED29.red_anode, LED30.red_anode, LED31.red_anode, LED32.red_anode, U2.Q4
  N29: LED33.red_anode, LED34.red_anode, LED35.red_anode, LED36.red_anode, LED37.red_anode, LED38.red_anode, LED39.red_anode, LED40.red_anode, U2.Q3
  N30: LED41.red_anode, LED42.red_anode, LED43.red_anode, LED44.red_anode, LED45.red_anode, LED46.red_anode, LED47.red_anode, LED48.red_anode, U2.Q2
  N31: LED49.red_anode, LED50.red_anode, LED51.red_anode, LED52.red_anode, LED53.red_anode, LED54.red_anode, LED55.red_anode, U2.Q1, LED56.red_anode
  N32: LED57.red_anode, LED58.red_anode, LED59.red_anode, LED60.red_anode, LED61.red_anode, LED62.red_anode, LED63.red_anode, LED64.red_anode, U2.Q0
  GND: U1.GND, U1.OE, Arduino1.GND, U2.GND, U2.OE, U3.GND, U3.OE, U4.GND, U4.OE
  VCC: U1.MR, U1.VCC, Arduino1.+5V, U2.MR, U2.VCC, U3.MR, U3.VCC, U4.MR, U4.VCC
  N33: U1.SH_CP, Arduino1.D10, U2.SH_CP
  N34: U1.ST_CP, Arduino1.D9, U2.ST_CP
  N35: U1.DS, U2.Q7'
  N36: Arduino1.D8, U2.DS
  N37: Arduino1.D6, U3.SH_CP, U4.SH_CP
  N38: Arduino1.D5, U3.ST_CP, U4.ST_CP
  N39: Arduino1.D4, U4.DS
  N40: U3.DS, U4.Q7'
