# Fritzing sketch id3402_Tastic_Custom_RFID_0 (saved by Fritzing 0.9.2b)
circuit board: 7.432cm x 4.86756cm
breadboards: 1

parts:
  LM317LZ1 = LM317LZ_Variable_Voltage_Regulator_TO_92_v2
  VCC1 = Battery  # not connected
  VCC2 = Battery  # not connected
  VCC3 = Battery
  VCC4 = Battery  # not connected
  VCC5 = Battery  # not connected
  VCC6 = Battery  # not connected
  R2_-_2000Ω = Resistor [tolerance=±5% resistance=2k package=THT]
  R1_-_268Ω = Resistor [tolerance=±5% resistance=268 package=THT]
  MaxiProx = Screw_terminal___4_pins
  LCD_Screw_Terminal = screw terminal, 3 pins
  18V_Battery = screw terminal, 2 pins
  Serial-LCD1 = Serial_20_X_4_LCD_Module [part_number=LCM2004D3-NSW-BBW]
  Toggle_Switch_(2_pin)1 = Toggle_Switch___2_Pin
  100uF_50V = Electrolytic Capacitor [capacitance=100μF voltage=50V package="100 mil [THT, electrolytic]"]
  Arduino_Nano_3_0 = Arduino Nano (Rev3.0)
  microSD_Transflash1 = SparkFun - microSD Transflash

nets:
  N1: LM317LZ1.connector0, R2_-_2000Ω.Pin_0, R1_-_268Ω.Pin_0
  N2: LM317LZ1.connector1, R1_-_268Ω.Pin_1, 100uF_50V.+, Arduino_Nano_3_0.VIN
  N3: LM317LZ1.connector2, MaxiProx.connector2, 18V_Battery.pin2, Toggle_Switch_(2_pin)1.connector2
  N4: VCC3.-, R2_-_2000Ω.Pin_1, MaxiProx.connector3, LCD_Screw_Terminal.pin2, 18V_Battery.pin1, Serial-LCD1.connector1, 100uF_50V.-, microSD_Transflash1.GND
  N5: MaxiProx.connector0, Arduino_Nano_3_0.D3
  N6: MaxiProx.connector1, Arduino_Nano_3_0.D2
  N7: LCD_Screw_Terminal.pin1, Serial-LCD1.connector0, Arduino_Nano_3_0.D4
  N8: LCD_Screw_Terminal.pin3, Serial-LCD1.connector2, Arduino_Nano_3_0.5V
  N9: Arduino_Nano_3_0.D10, microSD_Transflash1.CS
  N10: Arduino_Nano_3_0.D12/MISO, microSD_Transflash1.DO

notes:
  MaxiProx Pins
  - Red: 18 volt DC input
  - Black: Ground
  - Green: Data 0
  - White: Data 1
  **Note: all devices have to use the SAME GROUND, or results get funky
  12 X AA Batteries in series for 18 V DC]
  Voltage Conversion
  - Reducing 18V down to ~10V-11V
  - LM317LZ - Voltage Regulator
  - R1 = 268Ω
  - R2 = 2000Ω
  - 100uF 50V Capacitor (smooths voltage)
  Pins: Arduino -> MicroSD:
  - D10 -> CS
  - D11 -> DI
  - D12 -> DO
  - D13 -> SCK
  - 3V3 -> VCC
  Pins: Arduino -> SerialLCD 20x4:
  - D4 -> RX
  - +5V -> VDD
  Pins: Arduino -> Maxiprox 5375AGN00:
  - D2 -> Data 0 (green)
  - D3 -> Data 1 (white)
  Power Summary
  - 18V DC -> MaxiProx
  - ~10-11V DC -> Arduino Nano (VIN pin)
  - 3.3V -> MicroSD Transflash
  - 5.0V -> Serial LCD 20x4
  +
  -
  RX
  VSS
  VDD
  Data 0
  Data 1
  By Tastic
  www.bishopfox.com
  RFID Stealer
