# Fritzing sketch id3403_RFID_servo_controller_0 (saved by Fritzing 0.9.3b)
breadboards: 1

parts:
  rfid = RFID-RC522
  uno = Arduino Uno (Rev3)
  J1 = Piezo Speaker
  LED1 = LED - 5mm [color="Green (555nm)" package="5 mm [THT]"]
  LED2 = LED - 5mm [color="Red (635nm)" package="5 mm [THT]"]
  R1 = Resistor [tolerance=±5% resistance=220 package=THT]
  R2 = Resistor [tolerance=±5% resistance=220 package=THT]
  J2 = Basic Servo

nets:
  N1: rfid.connector8, uno.D10_PWM/SS
  N2: rfid.connector9, uno.D13/SCK
  N3: rfid.connector10, uno.D11_PWM/MOSI
  N4: rfid.connector11, uno.D12/MISO
  GND: rfid.connector13, uno.GND, J1.pin1, LED1.cathode, LED2.cathode, R1.Pin_0, R2.Pin_0, J2.gnd
  N5: rfid.connector14, uno.D9_PWM
  N6: rfid.connector15, uno.3V3
  N7: uno.D2, J1.pin2
  N8: uno.D3_PWM, J2.pulse
  N9: uno.D4, R1.Pin_1
  N10: uno.D5_PWM, R2.Pin_1
  5V: uno.5V, J2.vcc

notes:
  200 ohm resistors
