# Fritzing sketch id3404_RFID_Door_0 (saved by Fritzing 0.9.2b)

parts:
  neopixel1 = Neopixel_24_Ring
  LED1 = Adafruit_FLORA_RGB_Smart_Pixel
  S2 = SPST Switch [package=switch-spdt]
  BUTTON1 = Waterproof_Momentary_Pushbutton__red
  C1 = Capacitor Polarized [package=panasonic_g]
  U1 = ID-12_20 [package=id-12]
  Part3 = proto_shield_v5
  J3 = Piezo Speaker
  J1 = Basic Servo

nets:
  N1: neopixel1.connector1, Part3.connector25
  N2: neopixel1.connector2, Part3.connector221
  N3: neopixel1.connector3, Part3.connector81
  N4: neopixel1.connector4, LED1.connector2
  N5: LED1.connector1, Part3.connector215
  N6: LED1.connector3, Part3.connector24
  N7: S2.O, U1.D0
  N8: S2.P, Part3.connector75
  N9: BUTTON1.connector1, Part3.connector219
  N10: BUTTON1.connector3, Part3.connector66
  N11: BUTTON1.connector4, Part3.connector23
  N12: BUTTON1.connector5, Part3.connector27
  N13: C1.+, Part3.connector217, J1.vcc
  N14: U1.GNDT, Part3.connector16
  N15: U1.RES, Part3.connector82
  N16: U1.D1, Part3.connector20
  N17: U1.5V, Part3.connector225
  N18: Part3.connector26, J1.gnd
  N19: Part3.connector60, J3.pin1
  N20: Part3.connector63, J3.pin2
  N21: Part3.connector65, J1.pulse

notes:
  LED Button
  Speaker
  Neopixel
  Servo
  1000uF
  Neopixel Ring
  ID-20LA RFID
  VCC-READ-D0-D1-FORM-TIR
  GND-RES-ANT-ANT-CP
  All Red Wires go to 5V
  All Black Wires go to Ground
