# Fritzing sketch id3405_RFID_0 (saved by Fritzing 0.9.2b)
breadboards: 1

parts:
  R1 = Resistor [tolerance=±5% resistance=220 package=THT]
  LED1 = RGB LED (com. cathode, rgb) [package="5 mm [THT]"]
  SP1 = SPEAKER [package=pcb_mount_speaker]
  J1 = Basic Servo
  VCC2 = 4 x AAA Battery Mount
  Part1 = Arduino Uno (Rev3)  # not connected
  Part2 = Arduino Prototyping Shield

nets:
  GND: R1.Pin_0, SP1.+, J1.gnd, VCC2.-, Part2.GND
  N1: R1.Pin_1, LED1.common_cathode
  N2: LED1.red_anode, Part2.D4
  N3: LED1.green_anode, SP1.-, Part2.D5
  N4: LED1.blue_anode, Part2.D6
  N5: J1.vcc, VCC2.+
  N6: J1.pulse, Part2.D7
