# Fritzing sketch id3406_RGB_0 (saved by Fritzing 0.9.3b)
breadboards: 1

parts:
  Mosfet_driver_module1 = IRF520_mos_module
  Mosfet_driver_module2 = IRF520_mos_module
  Componente1 = Arduino Uno (Rev3)
  RGB_Strip_LED1 = RGB Strip LED
  VCC6 = Battery
  VCC7 = Battery
  VCC8 = Battery
  VCC9 = Battery
  Mosfet_driver_module3 = IRF520_mos_module

nets:
  N1: Mosfet_driver_module1.connector0, Componente1.D9_PWM
  N2: Mosfet_driver_module1.connector2, Mosfet_driver_module1.connector6, Mosfet_driver_module2.connector2, Mosfet_driver_module2.connector6, Componente1.GND, VCC9.-, Mosfet_driver_module3.connector2, Mosfet_driver_module3.connector6
  N3: Mosfet_driver_module1.connector4, RGB_Strip_LED1.connector9
  N4: Mosfet_driver_module1.connector5, Mosfet_driver_module2.connector5, Componente1.VIN, RGB_Strip_LED1.connector8, VCC6.+, Mosfet_driver_module3.connector5
  N5: Mosfet_driver_module2.connector0, Componente1.D10_PWM/SS
  N6: Mosfet_driver_module2.connector4, RGB_Strip_LED1.connector10
  N7: Componente1.D11_PWM/MOSI, Mosfet_driver_module3.connector0
  N8: RGB_Strip_LED1.connector11, Mosfet_driver_module3.connector4
  N9: VCC6.-, VCC7.+
  N10: VCC7.-, VCC8.+
  N11: VCC8.-, VCC9.+
