# Fritzing sketch id3407_RGB1_0 (saved by Fritzing 0.9.3b)
breadboards: 1

parts:
  Power_-_12V = Power plug
  Componente1 = Arduino Uno (Rev3) - ICSP
  IC1 = ULN2803A [package=THT]
  RGB_Strip_LED2 = RGB Strip LED

nets:
  GND: Power_-_12V.GND, Componente1.GND, IC1.0V, IC1.COM_-_Common
  VCC: Power_-_12V.VCC, Componente1.VIN, RGB_Strip_LED2.connector8
  N1: Componente1.D9_PWM, IC1.In_3, IC1.Out_3, RGB_Strip_LED2.connector11
  N2: Componente1.D10_PWM/SS, IC1.In_2, IC1.Out_2, RGB_Strip_LED2.connector10
  N3: Componente1.D11_PWM/MOSI, IC1.In_1, IC1.Out_1, RGB_Strip_LED2.connector9
  N4: IC1.In_4, IC1.Out_4
  N5: IC1.In_5, IC1.Out_5
  N6: IC1.In_6, IC1.Out_6
  N7: IC1.In_7, IC1.Out_7
  N8: IC1.In_8, IC1.Out_8
