# Fritzing sketch id3408_RGB_3x3x3_LED_CUBE_0 (saved by Fritzing 0.7.10b)

parts:
  Q1 = NPN-Transistor [package="TO92 [THT]"]
  Q2 = NPN-Transistor [package="TO92 [THT]"]
  Q3 = NPN-Transistor [package="TO92 [THT]"]
  Q4 = NPN-Transistor [package="TO92 [THT]"]
  Q5 = NPN-Transistor [package="TO92 [THT]"]
  Q6 = NPN-Transistor [package="TO92 [THT]"]
  Q8 = NPN-Transistor [package="TO92 [THT]"]
  Q9 = NPN-Transistor [package="TO92 [THT]"]
  U1 = atmega168 [package=dip]
  IC1 = ULN2003A [package="DIP16 [THT]"]
  XTAL1 = Crystal [frequency="16 Mhz" package=THT]
  LED1 = RGB LED (com. cathode, rbg) [package="5 mm [THT]"]
  LED4 = RGB LED (com. cathode, rbg) [package="5 mm [THT]"]
  LED3 = RGB LED (com. cathode, rbg) [package="5 mm [THT]"]
  LED2 = RGB LED (com. cathode, rbg) [package="5 mm [THT]"]
  LED5 = RGB LED (com. cathode, rbg) [package="5 mm [THT]"]
  LED6 = RGB LED (com. cathode, rbg) [package="5 mm [THT]"]
  LED7 = RGB LED (com. cathode, rbg) [package="5 mm [THT]"]
  LED8 = RGB LED (com. cathode, rbg) [package="5 mm [THT]"]
  LED9 = RGB LED (com. cathode, rbg) [package="5 mm [THT]"]
  C2 = Ceramic Capacitor [capacitance=2.2µF package="100 mil [THT, multilayer]"]
  C3 = Ceramic Capacitor [capacitance=2.2µF package="100 mil [THT, multilayer]"]
  C4 = Electrolytic Capacitor [capacitance=10µF package="100 mil [THT, electrolytic]"]
  R1 = Resistor [tolerance=±5% resistance=1k package=THT]
  R2 = Resistor [tolerance=±5% resistance=1k package=THT]
  R3 = Resistor [tolerance=±5% resistance=1k package=THT]
  R4 = Resistor [tolerance=±5% resistance=1k package=THT]
  R5 = Resistor [tolerance=±5% resistance=1k package=THT]
  R6 = Resistor [tolerance=±5% resistance=1k package=THT]
  R7 = Resistor [tolerance=±5% resistance=1k package=THT]
  R8 = Resistor [tolerance=±5% resistance=1k package=THT]
  R9 = Resistor [tolerance=±5% resistance=1k package=THT]
  R10 = Resistor [tolerance=±5% resistance=10k package=THT]
  R11 = Resistor [tolerance=±5% resistance=220 package=THT]
  R12 = Resistor [tolerance=±5% resistance=220 package=THT]
  R13 = Resistor [tolerance=±5% resistance=220 package=THT]
  R14 = Resistor [tolerance=±5% resistance=220 package=THT]
  R15 = Resistor [tolerance=±5% resistance=220 package=THT]
  R16 = Resistor [tolerance=±5% resistance=220 package=THT]
  R17 = Resistor [tolerance=±5% resistance=220 package=THT]
  R18 = Resistor [tolerance=±5% resistance=220 package=THT]
  R19 = Resistor [tolerance=±5% resistance=220 package=THT]
  Power_plug1 = Power plug
  Q7 = NPN-Transistor [package="TO92 [THT]"]

nets:
  GND: Q1.E, Q2.E, Q3.E, Q4.E, Q5.E, Q6.E, Q8.E, Q9.E, U1.GND, IC1.In_4, IC1.In_5, IC1.0V, C2.0, C3.0, R10.Pin_1, Power_plug1.GND, Q7.E
  N1: Q1.B, R2.Pin_1
  N2: Q1.C, LED8.common_cathode
  N3: Q2.B, R6.Pin_1
  N4: Q2.C, LED4.common_cathode
  N5: Q3.B, R3.Pin_1
  N6: Q3.C, LED7.common_cathode
  N7: Q4.B, R1.Pin_1
  N8: Q4.C, LED9.common_cathode
  N9: Q5.B, R7.Pin_1
  N10: Q5.C, LED3.common_cathode
  N11: Q6.B, R4.Pin_1
  N12: Q6.C, LED6.common_cathode
  N13: Q8.B, R5.Pin_1
  N14: Q8.C, LED5.common_cathode
  N15: Q9.B, R9.Pin_1
  N16: Q9.C, LED1.common_cathode
  N17: U1.RESET, R10.Pin_0
  N18: U1.D2, R17.Pin_0
  N19: U1.D3_(PWM), R13.Pin_0
  N20: U1.D4, R14.Pin_0
  N21: U1.VCC, IC1.Out_1, C4.+
  N22: U1.XLAT1, XTAL1.pin_1, C3.1
  N23: U1.XLAT2, XTAL1.pin_0, C2.1
  N24: U1.D5_(PWM), R11.Pin_0
  N25: U1.D6_(PWM), R12.Pin_0
  N26: U1.D7, R16.Pin_0
  N27: U1.D8, IC1.In_6
  N28: U1.D9_(PWM), R18.Pin_0
  N29: U1.D10_(PWM), R15.Pin_0
  N30: U1.A1, R1.Pin_0
  N31: U1.A2, IC1.In_1
  N32: U1.A3, IC1.In_2
  N33: U1.A4, IC1.In_3
  N34: U1.A5, R19.Pin_0
  N35: IC1.In_7, R2.Pin_0
  N36: IC1.COM_-_Common, R3.Pin_0
  N37: IC1.Out_7, R4.Pin_0
  N38: IC1.Out_6, R5.Pin_0
  N39: IC1.Out_5, R6.Pin_0
  N40: IC1.Out_4, R7.Pin_0
  N41: IC1.Out_3, R8.Pin_0
  N42: IC1.Out_2, R9.Pin_0
  N43: LED1.red_anode, LED3.red_anode, LED2.red_anode, R18.Pin_1
  N44: LED1.blue_anode, LED3.blue_anode, LED2.blue_anode, R12.Pin_1
  N45: LED1.green_anode, LED3.green_anode, LED2.green_anode, R13.Pin_1
  N46: LED4.red_anode, LED5.red_anode, LED6.red_anode, R15.Pin_1
  N47: LED4.blue_anode, LED5.blue_anode, LED6.blue_anode, R16.Pin_1
  N48: LED4.green_anode, LED5.green_anode, LED6.green_anode, R14.Pin_1
  N49: LED2.common_cathode, Q7.C
  N50: LED7.red_anode, LED8.red_anode, LED9.red_anode, R17.Pin_1
  N51: LED7.blue_anode, LED8.blue_anode, LED9.blue_anode, R19.Pin_1
  N52: LED7.green_anode, LED8.green_anode, LED9.green_anode, R11.Pin_1
  N53: C4.-, Power_plug1.VCC
  N54: R8.Pin_1, Q7.B
