# Fritzing sketch id3409_RGB_0 (saved by Fritzing 0.9.2b)
breadboards: 1

parts:
  Часть1 = Arduino Uno (Rev3)
  LED1 = RGB LED (com. cathode, rgb) [package="5 mm [THT]"]
  S1 = Pushbutton [package="[SMD]"]
  R1 = Resistor [tolerance=±5% resistance=10k package="1206 [SMD]"]
  R4 = Resistor [tolerance=±5% resistance=220 package="1206 [SMD]"]
  R5 = Resistor [tolerance=±5% resistance=220 package="1206 [SMD]"]
  R6 = Resistor [tolerance=±5% resistance=220 package="1206 [SMD]"]

nets:
  N1: Часть1.D9_PWM, R5.Pin_0
  N2: Часть1.D3_PWM, S1.Pin_3, S1.Pin_4, R1.Pin_0
  N3: Часть1.D5_PWM, R6.Pin_0
  N4: Часть1.D6_PWM, R4.Pin_0
  N5: Часть1.5V, S1.Pin_1, S1.Pin_2
  N6: Часть1.GND, LED1.common_cathode, R1.Pin_1
  N7: LED1.red_anode, R6.Pin_1
  N8: LED1.green_anode, R5.Pin_1
  N9: LED1.blue_anode, R4.Pin_1
