# Fritzing sketch id340_Master_Led_Controller_0 (saved by Fritzing 0.9.3b)
circuit board: 6.85cm x 7.35cm
breadboards: 1

parts:
  Max7219 = MAX7219 [package=dil24]
  R1 = Resistor [tolerance=±5% resistance=10 package=THT]
  C1 = Ceramic Capacitor [capacitance=0.1µF package="100 mil [THT, multilayer]"]
  C2 = Electrolytic Capacitor [capacitance=10µF package="100 mil [THT, electrolytic]"]
  Arduino = Arduino Uno (Rev3)  # not connected
  D0 = female pin header, 9 pins [form="♀ (female)"]
  D4 = female pin header, 9 pins [form="♀ (female)"]
  D6 = female pin header, 9 pins [form="♀ (female)"]
  D2 = female pin header, 9 pins [form="♀ (female)"]
  D3 = female pin header, 9 pins [form="♀ (female)"]
  D1 = female pin header, 9 pins [form="♀ (female)"]
  D7 = female pin header, 9 pins [form="♀ (female)"]
  J1 = female pin header, 5 pins [form="♀ (female)"]
  D5 = female pin header, 9 pins [form="♀ (female)"]
  Max7219_2 = MAX7219 [package=dil24]
  R2 = Resistor [tolerance=±5% resistance=10 package=THT]
  C3 = Ceramic Capacitor [capacitance=0.1µF package="100 mil [THT, multilayer]"]
  C4 = Electrolytic Capacitor [capacitance=10µF package="100 mil [THT, electrolytic]"]
  D7_2 = female pin header, 9 pins [form="♀ (female)"]
  D5_2 = female pin header, 9 pins [form="♀ (female)"]
  D1_2 = female pin header, 9 pins [form="♀ (female)"]
  D3_2 = female pin header, 9 pins [form="♀ (female)"]
  D2_2 = female pin header, 9 pins [form="♀ (female)"]
  D6_2 = female pin header, 9 pins [form="♀ (female)"]
  D4_2 = female pin header, 9 pins [form="♀ (female)"]
  D0_2 = female pin header, 9 pins [form="♀ (female)"]

nets:
  N1: Max7219.DIN, J1.pin3
  N2: Max7219.DIG0, D0.pin1
  N3: Max7219.DIG4, D4.pin1
  GND: Max7219.GND, Max7219.GND2, C1.0, C2.-, J1.pin1, Max7219_2.GND, Max7219_2.GND2, C3.0, C4.-
  N4: Max7219.DIG6, D6.pin1
  N5: Max7219.DIG2, D2.pin1
  N6: Max7219.DIG3, D3.pin1
  N7: Max7219.DIG7, D7.pin1
  N8: Max7219.DIG5, D5.pin1
  N9: Max7219.DIG1, D1.pin1
  N10: Max7219.LOAD, J1.pin2, Max7219_2.LOAD
  N11: Max7219.CLK, J1.pin5, Max7219_2.CLK
  N12: Max7219.SEGA, D0.pin9, D4.pin9, D6.pin9, D2.pin9, D3.pin9, D1.pin9, D7.pin9, D5.pin9
  N13: Max7219.SEGF, D0.pin8, D4.pin8, D6.pin8, D2.pin8, D3.pin8, D1.pin8, D7.pin8, D5.pin8
  N14: Max7219.SEGB, D0.pin7, D4.pin7, D6.pin7, D2.pin7, D3.pin7, D1.pin7, D7.pin7, D5.pin7
  N15: Max7219.SEGG, D0.pin6, D4.pin6, D6.pin6, D2.pin6, D3.pin6, D1.pin6, D7.pin6, D5.pin6
  N16: Max7219.ISET, R1.Pin_1
  VCC: Max7219.VCC, R1.Pin_0, C1.1, C2.+, J1.pin4, Max7219_2.VCC, R2.Pin_0, C3.1, C4.+
  N17: Max7219.SEGC, D0.pin4, D4.pin4, D6.pin4, D2.pin4, D3.pin4, D1.pin4, D7.pin4, D5.pin4
  N18: Max7219.SEGE, D0.pin5, D4.pin5, D6.pin5, D2.pin5, D3.pin5, D1.pin5, D7.pin5, D5.pin5
  N19: Max7219.SEGDP, D0.pin2, D4.pin2, D6.pin2, D2.pin2, D3.pin2, D1.pin2, D7.pin2, D5.pin2
  N20: Max7219.SEGD, D0.pin3, D4.pin3, D6.pin3, D2.pin3, D3.pin3, D1.pin3, D7.pin3, D5.pin3
  N21: Max7219.DOUT, Max7219_2.DIN
  N22: Max7219_2.DIG0, D0_2.pin1
  N23: Max7219_2.DIG4, D4_2.pin1
  N24: Max7219_2.DIG6, D6_2.pin1
  N25: Max7219_2.DIG2, D2_2.pin1
  N26: Max7219_2.DIG3, D3_2.pin1
  N27: Max7219_2.DIG7, D7_2.pin1
  N28: Max7219_2.DIG5, D5_2.pin1
  N29: Max7219_2.DIG1, D1_2.pin1
  N30: Max7219_2.SEGA, D7_2.pin9, D5_2.pin9, D1_2.pin9, D3_2.pin9, D2_2.pin9, D6_2.pin9, D4_2.pin9, D0_2.pin9
  N31: Max7219_2.SEGF, D7_2.pin8, D5_2.pin8, D1_2.pin8, D3_2.pin8, D2_2.pin8, D6_2.pin8, D4_2.pin8, D0_2.pin8
  N32: Max7219_2.SEGB, D7_2.pin7, D5_2.pin7, D1_2.pin7, D3_2.pin7, D2_2.pin7, D6_2.pin7, D4_2.pin7, D0_2.pin7
  N33: Max7219_2.SEGG, D7_2.pin6, D5_2.pin6, D1_2.pin6, D3_2.pin6, D2_2.pin6, D6_2.pin6, D4_2.pin6, D0_2.pin6
  N34: Max7219_2.ISET, R2.Pin_1
  N35: Max7219_2.SEGC, D7_2.pin4, D5_2.pin4, D1_2.pin4, D3_2.pin4, D2_2.pin4, D6_2.pin4, D4_2.pin4, D0_2.pin4
  N36: Max7219_2.SEGE, D7_2.pin5, D5_2.pin5, D1_2.pin5, D3_2.pin5, D2_2.pin5, D6_2.pin5, D4_2.pin5, D0_2.pin5
  N37: Max7219_2.SEGDP, D7_2.pin2, D5_2.pin2, D1_2.pin2, D3_2.pin2, D2_2.pin2, D6_2.pin2, D4_2.pin2, D0_2.pin2
  N38: Max7219_2.SEGD, D7_2.pin3, D5_2.pin3, D1_2.pin3, D3_2.pin3, D2_2.pin3, D6_2.pin3, D4_2.pin3, D0_2.pin3

notes:
  VCC
  CLK
  DIN
  CS
  GND
  0.1µF
  10µF
  10K
  DP
  D
  C
  E
  G
  B
  F
  A
  Led Controller V1.0
  Ricardo Amado
