# Fritzing sketch id3410_E4_EyS_Analog_0 (saved by Fritzing 0.9.2b)
breadboards: 1

parts:
  R1 = Resistor [tolerance=±5% resistance=220 package=THT]
  R1_2 = Rotary Potentiometer (Small) [maximum_resistance=10kΩ package=THT]
  LED1 = RGB LED (com. cathode, rgb) [package="5 mm [THT]"]
  Parte1 = Arduino Uno (Rev3)
  R3 = Rotary Potentiometer (Small) [maximum_resistance=10kΩ package=THT]
  R2 = Rotary Potentiometer (Small) [maximum_resistance=10kΩ package=THT]
  R4 = Resistor [tolerance=±5% resistance=100 package=THT]
  R5 = Resistor [tolerance=±5% resistance=100 package=THT]
  S1 = Pushbutton [package="[THT]"]
  R6 = Resistor [tolerance=±5% resistance=10k package=THT]

nets:
  N1: R1.Pin_0, LED1.red_anode
  N2: R1.Pin_1, Parte1.D11_PWM/MOSI
  N3: R1_2.leg1, Parte1.5V, R3.leg1, R2.leg1, S1.Pin_3, S1.Pin_4
  N4: R1_2.wiper, Parte1.A2
  N5: R1_2.leg2, LED1.common_cathode, Parte1.GND, R3.leg2, R2.leg2, R6.Pin_1
  N6: LED1.green_anode, R5.Pin_1
  N7: LED1.blue_anode, R4.Pin_1
  N8: Parte1.A0, R3.wiper
  N9: Parte1.A1, R2.wiper
  N10: Parte1.D9_PWM, R4.Pin_0
  N11: Parte1.D10_PWM/SS, R5.Pin_0
  N12: Parte1.D2, S1.Pin_1, S1.Pin_2, R6.Pin_0
