# Fritzing sketch id3411_RGB_Joystick_Controller_0 (saved by Fritzing 0.7.10b)
breadboards: 1

parts:
  Arduino1 = Arduino
  Parte1 = Thumb Joystick
  Parte2 = Thumb Joystick
  LED1 = Super Flux RGB LED (com. anode)

nets:
  N1: Arduino1.D6, LED1.blue_cathode
  N2: Arduino1.D5, LED1.green_cathode
  N3: Arduino1.D3, LED1.red_cathode
  VCC: Arduino1.+5V, Parte1.VCC, Parte2.VCC, LED1.common_anode
  GND: Arduino1.GND, Parte1.GND, Parte2.GND
  N4: Arduino1.A0, Parte1.HORZ
  N5: Arduino1.A1, Parte1.VERT
  N6: Arduino1.A2, Parte2.HORZ
