# Fritzing sketch id3412_RGB_Driver_V1_0 (saved by Fritzing 0.7.4b)
stripboards: 1

parts:
  part = female pin header, 2 pins [form="♀ (female)" part_number=Voeding]
  R3 = Resistor [tolerance=±5% resistance=10 package="0805 [SMD]"]
  R2 = Resistor [tolerance=±5% resistance=4.7 package="0805 [SMD]"]
  R1 = Resistor [tolerance=±5% resistance=4.7 package="0805 [SMD]"]
  R4 = Resistor [tolerance=±5% resistance=470 package="0805 [SMD]"]
  Q2 = NPN-Transistor [package="SOT-23 [SMD]"]
  Q3 = NPN-Transistor [package="SOT-23 [SMD]"]
  R5 = Resistor [tolerance=±5% resistance=470 package="0805 [SMD]"]
  Q1 = NPN-Transistor [package="SOT-23 [SMD]"]
  R6 = Resistor [tolerance=±5% resistance=470 package="0805 [SMD]"]
  Out = female pin header, 4 pins [form="♀ (female)"]
  In = female pin header, 3 pins [form="♀ (female)"]
  USB = female pin header, 4 pins [form="♀ (female)"]
  J7 = female pin header, 1 pin [form="♀ (female)"]
  J9 = female pin header, 1 pin [form="♀ (female)"]

nets:
  N1: part.pin1, Q2.2, Q3.2, Q1.2, USB.pin1, J7.pin1, J9.pin1
  N2: part.pin2, Out.pin1, USB.pin4
  N3: R3.Pin_0, Out.pin2
  N4: R3.Pin_1, Q3.1
  N5: R2.Pin_0, Out.pin3
  N6: R2.Pin_1, Q2.1
  N7: R1.Pin_0, Out.pin4
  N8: R1.Pin_1, Q1.1
  N9: R4.Pin_0, Q3.0
  N10: R4.Pin_1, In.pin1
  N11: Q2.0, R5.Pin_0
  N12: R5.Pin_1, In.pin2
  N13: Q1.0, R6.Pin_0
  N14: R6.Pin_1, In.pin3

notes:
  GND
  VCC
  Gnd
  +5V
  RGB Driver V1
  Power
  R
  G
  B
  +
