# Fritzing sketch id3413_AnalogReadSerial2LCD_LED_0 (saved by Fritzing 0.9.3b)
circuit board: 8.46667cm x 5.64444cm
breadboards: 1

parts:
  Onderdeel1 = Arduino Uno (Rev3)
  LCM1602_IIC1 = generic_ic_dip_22_300mil.fzp [part_number="LCM1602 IIC" chip_label="LCM1602 IIC"]
  LCD1 = LCD screen
  R1 = Trimmer Potentiometer [maximum_resistance=10kΩ package=THT]
  NEOPIXEL3 = adafruit [part_number=1461]
  R2 = Trimmer Potentiometer [maximum_resistance=10kΩ package=THT]
  R3 = Trimmer Potentiometer [maximum_resistance=10kΩ package=THT]

nets (from the breadboard view):
  N1: Onderdeel1.A0, R1.wiper
  N2: Onderdeel1.A1, R3.wiper
  N3: Onderdeel1.A2, R2.wiper
  N4: Onderdeel1.A4/SDA, LCM1602_IIC1.connector18
  N5: Onderdeel1.A5/SCL, LCM1602_IIC1.connector19
  N6: Onderdeel1.D6_PWM, NEOPIXEL3.connector2
  N7: Onderdeel1.5V, LCM1602_IIC1.connector17, R1.leg2, NEOPIXEL3.connector6, R2.leg2, R3.leg2
  N8: Onderdeel1.GND, LCM1602_IIC1.connector16, R1.leg1, NEOPIXEL3.connector4, R2.leg1, R3.leg1
  N9: LCM1602_IIC1.connector0, LCD1.VSS
  N10: LCM1602_IIC1.connector1, LCD1.VDD
  N11: LCM1602_IIC1.connector2, LCD1.V0
  N12: LCM1602_IIC1.connector3, LCD1.RS
  N13: LCM1602_IIC1.connector4, LCD1.R/W
  N14: LCM1602_IIC1.connector5, LCD1.E
  N15: LCM1602_IIC1.connector6, LCD1.DB0
  N16: LCM1602_IIC1.connector7, LCD1.DB1
  N17: LCM1602_IIC1.connector8, LCD1.DB2
  N18: LCM1602_IIC1.connector9, LCD1.DB3
  N19: LCM1602_IIC1.connector10, LCD1.DB4
  N20: LCM1602_IIC1.connector11, LCD1.DB5
  N21: LCM1602_IIC1.connector12, LCD1.DB6
  N22: LCM1602_IIC1.connector13, LCD1.DB7
  N23: LCM1602_IIC1.connector14, LCD1.LED+
  N24: LCM1602_IIC1.connector15, LCD1.LED-
  N25: LCM1602_IIC1.connector20, LCM1602_IIC1.connector21
