# Fritzing sketch id3414_Lampara_RGB_0 (saved by Fritzing 0.9.2b)
breadboards: 1

parts:
  Part1 = Arduino Uno (Rev3)
  R1 = Resistor [tolerance=±5% resistance=220 package=THT]
  R2 = Resistor [tolerance=±5% resistance=220 package=THT]
  R3 = Resistor [tolerance=±5% resistance=220 package=THT]
  R4 = Rotary Potentiometer (Small) [maximum_resistance=100kΩ package=THT]
  R5 = Rotary Potentiometer (Small) [maximum_resistance=100kΩ package=THT]
  R6 = Rotary Potentiometer (Small) [maximum_resistance=100kΩ package=THT]
  LED1 = RGB LED (com. cathode, rgb) [package="5 mm [THT]"]

nets:
  N1: Part1.A0, R4.wiper
  N2: Part1.A1, R5.wiper
  N3: Part1.A2, R6.wiper
  N4: Part1.D8, R1.Pin_1
  N5: Part1.D9_PWM, R3.Pin_1
  N6: Part1.D10_PWM/SS, R2.Pin_1
  N7: Part1.5V, R4.leg2, R5.leg2, R6.leg2
  N8: Part1.GND, R4.leg1, R5.leg1, R6.leg1, LED1.common_cathode
  N9: R1.Pin_0, LED1.blue_anode
  N10: R2.Pin_0, LED1.green_anode
  N11: R3.Pin_0, LED1.red_anode
