# Fritzing sketch id3416_Untitled_Sketch_0 (saved by Fritzing 0.8.7b)
breadboards: 1

parts:
  Part1 = Arduino Leonardo (Rev3b)
  R1 = Rotary Potentiometer (Large) [maximum_resistance=100kΩ package=THT]
  R2 = Resistor [tolerance=±5% resistance=360 package=THT]
  S1 = Pushbutton [package="[THT]"]
  R3 = Resistor [tolerance=±5% resistance=10k package=THT]
  LED1 = RGB LED - (4 legs) [package="5 mm [THT]"]  # not connected

nets:
  N1: Part1.5V, S1.Pin_3, S1.Pin_4
  N2: Part1.GND, R1.leg1, R3.Pin_0
  N3: R1.wiper, R2.Pin_0
  N4: R1.leg2, S1.Pin_1, S1.Pin_2, R3.Pin_1
