# Fritzing sketch id3417_RGB_LED_0 (saved by Fritzing 0.8.7b)
breadboards: 1

parts:
  LED1 = RGB LED (com. cathode, rgb) [package="5 mm [THT]"]
  R1 = Resistor [tolerance=±5% resistance=220 package=THT]
  Part1 = Arduino Uno (Rev3)
  R2 = Resistor [tolerance=±5% resistance=220 package=THT]
  R3 = Resistor [tolerance=±5% resistance=220 package=THT]

nets:
  N1: LED1.red_anode, R1.Pin_0
  N2: LED1.common_cathode, Part1.GND
  N3: LED1.green_anode, R2.Pin_0
  N4: LED1.blue_anode, R3.Pin_0
  N5: R1.Pin_1, Part1.D10_PWM/SS
  N6: Part1.D8, R3.Pin_1
  N7: Part1.D9_PWM, R2.Pin_1

notes:
  Components:
  1) Arduino UNO
  2) RGB LED
  3) 3 Resistors (220 Ohm)
  4) Wires
