# Fritzing sketch id3418_RGB_LED_and_POT_0 (saved by Fritzing 0.9.3b)
circuit board: 6.88566cm x 5.36311cm
breadboards: 1

parts:
  LED = RGB LED (com. cathode, rgb) [package="5 mm [THT]"]
  Arduino1 = Arduino Uno (Rev3)
  R6 = Resistor [tolerance=±5% resistance=220 package=THT]
  R5 = Resistor [tolerance=±5% resistance=220 package=THT]
  R4 = Resistor [tolerance=±5% resistance=220 package=THT]
  R8 = Rotary Potentiometer (Small) [maximum_resistance=100kΩ package=THT]

nets:
  N1: LED.red_anode, R4.Pin_1
  N2: LED.common_cathode, Arduino1.GND, R8.leg1
  N3: LED.green_anode, R6.Pin_1
  N4: LED.blue_anode, R5.Pin_1
  N5: Arduino1.A0, R8.wiper
  N6: Arduino1.D9_PWM, R5.Pin_0
  N7: Arduino1.D10_PWM/SS, R6.Pin_0
  N8: Arduino1.D11_PWM/MOSI, R4.Pin_0
  N9: Arduino1.5V, R8.leg2

notes:
  Use either the brown, four stripe resistors, or the blue, five stripe resistors. The color code for the brown one is red, red, brown, gold.
  220 ohm
