# Fritzing sketch id3419_Untitled_Sketch_0 (saved by Fritzing 0.9.2b)
circuit board: 1.19556cm x 1.08529cm
breadboards: 1

parts:
  LED1 = RGB LED (com. cathode, rgb) [package="5 mm [THT]"]
  R1 = Resistor [tolerance=±5% resistance=220 package=THT]
  J1 = male pin header, 4 pins [form="♂ (male)"]

nets:
  N1: LED1.red_anode, J1.pin2
  N2: LED1.common_cathode, R1.Pin_1
  N3: LED1.green_anode, J1.pin3
  N4: LED1.blue_anode, J1.pin4
  N5: R1.Pin_0, J1.pin1

notes:
  GND
  BLUE
  RED
  GREEN
