# Fritzing sketch id341_Nx64_Led_Controller_0 (saved by Fritzing 0.9.3b)
circuit board: 3.17cm x 4.88cm
breadboards: 1

parts:
  Max7219 = MAX7219 [package=dil24]
  D5 = female pin header, 9 pins [form="♀ (female)"]
  D6 = female pin header, 9 pins [form="♀ (female)"]
  J2 = female pin header, 5 pins [form="♀ (female)"]
  D2 = female pin header, 9 pins [form="♀ (female)"]
  D0 = female pin header, 9 pins [form="♀ (female)"]
  R1-10K = Resistor [tolerance=±5% resistance=10k package=THT]
  D1 = female pin header, 9 pins [form="♀ (female)"]
  J1 = female pin header, 5 pins [form="♀ (female)"]
  C2-10µF = Electrolytic Capacitor [capacitance=10µF package="100 mil [THT, electrolytic]"]  # not connected
  D3 = female pin header, 9 pins [form="♀ (female)"]
  D4 = female pin header, 9 pins [form="♀ (female)"]
  D7 = female pin header, 9 pins [form="♀ (female)"]
  C1-0_1µF = Ceramic Capacitor [capacitance=100nF package="100 mil [THT, multilayer]"]  # not connected

nets:
  N1: Max7219.DIN, J2.pin4
  N2: Max7219.DIG0, D0.pin1
  N3: Max7219.DIG4, D4.pin1
  N4: Max7219.DIG6, D6.pin1
  N5: Max7219.DIG2, D2.pin1
  N6: Max7219.DIG3, D3.pin1
  N7: Max7219.DIG7, D7.pin1
  N8: Max7219.DIG5, D5.pin1
  N9: Max7219.DIG1, D1.pin1
  N10: Max7219.LOAD, J2.pin5, J1.pin5
  N11: Max7219.CLK, J2.pin3, J1.pin3
  N12: Max7219.SEGA, D5.pin3, D6.pin3, D2.pin3, D0.pin3, D1.pin3, D3.pin3, D4.pin3, D7.pin3
  N13: Max7219.SEGF, D5.pin8, D6.pin8, D2.pin8, D0.pin8, D1.pin8, D3.pin8, D4.pin8, D7.pin8
  N14: Max7219.SEGB, D5.pin4, D6.pin4, D2.pin4, D0.pin4, D1.pin4, D3.pin4, D4.pin4, D7.pin4
  N15: Max7219.SEGG, D5.pin9, D6.pin9, D2.pin9, D0.pin9, D1.pin9, D3.pin9, D4.pin9, D7.pin9
  N16: Max7219.ISET, R1-10K.Pin_0
  N17: Max7219.SEGC, D5.pin5, D6.pin5, D2.pin5, D0.pin5, D1.pin5, D3.pin5, D4.pin5, D7.pin5
  N18: Max7219.SEGE, D5.pin7, D6.pin7, D2.pin7, D0.pin7, D1.pin7, D3.pin7, D4.pin7, D7.pin7
  N19: Max7219.SEGDP, D5.pin2, D6.pin2, D2.pin2, D0.pin2, D1.pin2, D3.pin2, D4.pin2, D7.pin2
  N20: Max7219.SEGD, D5.pin6, D6.pin6, D2.pin6, D0.pin6, D1.pin6, D3.pin6, D4.pin6, D7.pin6
  N21: Max7219.DOUT, J1.pin4

notes:
  CS
  VCC
  DIN
  G
  D
  GND
  10K
  E
  DP
  10µF
  A
  C
  F
  B
  CLK
  0.1µF
  LOAD
  v 0.0.15
  Design: Ricardo Amado
  DOUT
  Controller
  Nx64 Led
