# Fritzing sketch id3420_RGB_LED_CIRCUIT_0 (saved by Fritzing 0.9.3b)
breadboards: 1

parts:
  LED1 = RGB LED (com. anode, rbg) [package="5 mm [THT]"]
  Part1 = Arduino Uno (Rev3)
  R1 = Resistor [tolerance=±5% resistance=220 package="1206 [SMD]"]
  R2 = Resistor [tolerance=±5% resistance=220 package="1206 [SMD]"]
  R3 = Resistor [tolerance=±5% resistance=220 package="1206 [SMD]"]

nets:
  N1: LED1.red_cathode, R3.Pin_0
  N2: LED1.common_anode, R2.Pin_0
  N3: LED1.blue_cathode, Part1.5V
  N4: LED1.green_cathode, R1.Pin_0
  N5: Part1.D9_PWM, R3.Pin_1
  N6: Part1.D10_PWM/SS, R2.Pin_1
  N7: Part1.D11_PWM/MOSI, R1.Pin_1

notes:
  The Code
  int redPin = 11;
  int greenPin = 10;
  int bluePin = 9;
  int red=0,green=0,blue=0,redInput,greenInput,blueInput,redInput2,greenInput2,blueInput2;
  //uncomment this line if using a Common Anode LED
  //#define COMMON_ANODE
  void setup()
  {
  Serial.begin(115200);
  pinMode(redPin, OUTPUT);
  pinMode(greenPin, OUTPUT);
  pinMode(bluePin, OUTPUT);
  }
  void loop()
  {
  setColor(255,255,255);//white
  delay(1000);
  setColor(255,0,0);//red
  delay(1000);
  setColor(0,255,0);//green
  delay(1000);
  setColor(0,0,255);//blue
  delay(1000);
  }
  void setColor(int red, int green, int blue)
  {
  #ifdef COMMON_ANODE
  red = 255 - red;
  green = 255 - green;
  blue = 255 - blue;
  #endif
  analogWrite(redPin, red);
  analogWrite(greenPin, green);
  analogWrite(bluePin, blue);
  }
