# Fritzing sketch id3421_LED_RGB_ran_fritzing_0 (saved by Fritzing 0.9.3b)

parts:
  부품1 = Arduino Uno (Rev3)
  LED1 = RGB LED (com. cathode, rgb) [color="Red (633nm)" package="5 mm [THT]"]

nets:
  N1: 부품1.D9_PWM, LED1.red_anode
  N2: 부품1.D10_PWM/SS, LED1.green_anode
  N3: 부품1.D11_PWM/MOSI, LED1.blue_anode
  N4: 부품1.GND, LED1.common_cathode
