# Fritzing sketch id3422_RGB_led_2_0 (saved by Fritzing 0.9.3b)
breadboards: 1

parts:
  Součástka1 = Arduino Mega 2560 (Rev3)
  S2 = Momentary Switch [package=ksa_sealed_tac_switch]
  LED1 = RGB LED (com. cathode, rgb) [package="5 mm [THT]"]
  S3 = Momentary Switch [package=ksa_sealed_tac_switch]
  S4 = Momentary Switch [package=ksa_sealed_tac_switch]

nets:
  N1: Součástka1.5V, LED1.common_cathode
  N2: Součástka1.GND, S2.3, S3.1, S4.1
  N3: S2.2, LED1.blue_anode
  N4: LED1.red_anode, S4.2
  N5: LED1.green_anode, S3.2
