# Fritzing sketch id3424_Untitled_Sketch_0 (saved by Fritzing 0.9.1b)
circuit board: 8.46667cm x 5.64444cm
breadboards: 1

parts:
  RGB_LED = Arduino Uno (Rev3)
  LED1 = RGB LED (com. cathode, rgb) [package="5 mm [THT]"]
  R1 = Resistor [tolerance=±5% resistance=220 package=THT]
  R2 = Resistor [tolerance=±5% resistance=220 package=THT]
  R3 = Resistor [tolerance=±5% resistance=220 package=THT]

nets:
  N1: RGB_LED.D3_PWM, R3.Pin_1
  N2: RGB_LED.D5_PWM, R2.Pin_1
  N3: RGB_LED.D6_PWM, R1.Pin_1
  N4: RGB_LED.GND, LED1.common_cathode
  N5: LED1.red_anode, R1.Pin_0
  N6: LED1.green_anode, R2.Pin_0
  N7: LED1.blue_anode, R3.Pin_0

notes:
  RGB-каналы используют ШИМ
