# Fritzing sketch id3427_RGB_LED_0 (saved by Fritzing 0.9.3b)
breadboards: 1

parts:
  Q2 = NPN-Transistor [package="TO92 [THT]"]
  Q3 = NPN-Transistor [package="TO92 [THT]"]
  R1 = Resistor [tolerance=±5% resistance=15k package=THT]
  R4 = Resistor [tolerance=±5% resistance=680 package=THT]
  R5 = Resistor [tolerance=±5% resistance=15k package=THT]
  R6 = Resistor [tolerance=±5% resistance=15k package=THT]
  R7 = Resistor [tolerance=±5% resistance=680 package=THT]
  R8 = Resistor [tolerance=±5% resistance=680 package=THT]
  Uno = Arduino Uno (Rev3)
  LED1 = RGB LED (com. anode, rbg) [package="5 mm [THT]"]
  Q1 = NPN-Transistor [package="TO92 [THT]"]

nets:
  N1: Q2.E, Q3.E, Uno.GND, Q1.E
  N2: Q2.B, R7.Pin_1
  N3: Q2.C, R6.Pin_1
  N4: Q3.B, R8.Pin_1
  N5: Q3.C, R1.Pin_1
  N6: R1.Pin_0, LED1.blue_cathode
  N7: R4.Pin_0, Uno.D6_PWM
  N8: R4.Pin_1, Q1.B
  N9: R5.Pin_0, LED1.red_cathode
  N10: R5.Pin_1, Q1.C
  N11: R6.Pin_0, LED1.green_cathode
  N12: R7.Pin_0, Uno.D5_PWM
  N13: R8.Pin_0, Uno.D3_PWM
  N14: Uno.5V, LED1.common_anode

notes:
  This is an example of "low side" switching of LEDs using a transistor. Because the Arduino digital IO pins can sink as well as source current, this configuration isn't strictly necessary for most low current LEDs (you could just connect the LEDs' current limiting resistors directly to the Arduino's analog out pins).
  This configuration is useful, however if the LEDs you want to drive consume a higher current than the Arduino is able to sink (40mA max, probably shouldn't try to sink more than ~20mA though)
