# Fritzing sketch id342_Antenna_Rotator_0 (saved by Fritzing 0.9.2b)
breadboards: 1

parts:
  Componente1 = Arduino Pro Mini v13
  LCD1 = LCD screen
  M1 = DC Motor
  VCC1 = Battery block 9V
  U3 = Voltage Regulator - 5V [package="TO220 [THT]"]
  U5 = Optocoupler [package=THT]
  R3 = Resistor [tolerance=±5% resistance=4.7k package=THT]
  R4 = Resistor [tolerance=±5% resistance=4.7k package=THT]
  R5 = Resistor [tolerance=±5% resistance=1k package=THT]
  R6 = Trimmer Potentiometer [maximum_resistance=10kΩ package=THT]
  J2 = Infrared Proximity Sensor
  R7 = Rotary Potentiometer (Small) [maximum_resistance=100kΩ package=THT]
  U6 = L298 [package=multiwatt15_6400bgheatsink]
  R8 = Resistor [tolerance=±5% resistance=10k package=THT]
  R9 = Resistor [tolerance=±5% resistance=10k package=THT]
  U8 = LIPO-2000mAh [package=lipo-2000]
  U9 = LIPO-2000mAh [package=lipo-2000]
  U10 = LIPO-2000mAh [package=lipo-2000]
  J3 = Piezo Speaker
  RE1 = Rotary Encoder [package=THT]

nets:
  VCC: Componente1.VCC, LCD1.VDD, U3.output_voltage, U5.Pin_5, R6.leg2, J2.Vcc, R7.leg2, RE1.EncoderPinC
  N1: Componente1.A4, R7.wiper
  GND: Componente1.GND, LCD1.VSS, LCD1.R/W, LCD1.LED-, VCC1.-, R3.Pin_0, R4.Pin_0, R5.Pin_0, R6.leg1, J2.GND, R7.leg1, J3.pin1
  N2: Componente1.A3, LCD1.DB7
  N3: Componente1.A2, LCD1.DB6
  N4: Componente1.A1, LCD1.DB5
  N5: Componente1.A0, LCD1.DB4
  N6: Componente1.D12/MISO, LCD1.RS
  N7: Componente1.D11_PWM/MOSI, LCD1.E
  N8: Componente1.D10_PWM/SS, J3.pin2
  N9: Componente1.D9_PWM, U6.ENA
  N10: Componente1.D8, U6.IN2
  N11: Componente1.D7, U6.IN1
  N12: Componente1.D6_PWM, LCD1.LED+
  N13: Componente1.D4, U5.Pin_4
  N14: Componente1.D2, R8.Pin_1
  N15: LCD1.V0, R6.wiper
  N16: M1.pin_1, U6.OUT2
  N17: M1.pin_2, U6.OUT1
  N18: VCC1.+, U3.input_voltage
  N19: U5.Pin_1, J2.Vout
  N20: U5.Pin_2, R5.Pin_1
  N21: R3.Pin_1, R8.Pin_0, RE1.EncoderPinA
  N22: R4.Pin_1, R9.Pin_0, RE1.EncoderPinB
  N23: U8.-, U10.+
  N24: U9.+, U10.-
