# Fritzing sketch id3430_RGB_Mixer_0 (saved by Fritzing 0.3.13b)
breadboards: 1

parts:
  Arduino1 = Arduino
  R2 = Resistor [resistance=220 package=THT]
  R3 = Resistor [resistance=220 package=THT]
  R4 = Resistor [resistance=220 package=THT]
  LED1 = Red LED - 5mm
  LED2 = Blue LED - 5mm
  LED3 = Blue LED - 5mm
  LED4 = green LED - 5mm
  R5 = Resistor [resistance=220 package=THT]
  R6 = Resistor [resistance=220 package=THT]
  R7 = Resistor [resistance=220 package=THT]
  R8 = Resistor [resistance=220 package=THT]
  R10 = Resistor [resistance=1.1k package=THT]
  S2 = Pushbutton [package=THT]
  R11 = Resistor [resistance=1.1k package=THT]
  R1 = Resistor [resistance=220 package=THT]
  LED-RGB-Starter1 = RGB-LED-Starter
  S1 = Pushbutton [package=THT]
  R12 = Rotary Potentiometer (Large) [package=THT]

nets:
  N1: Arduino1.GND, LED1.cathode, LED2.cathode, LED3.cathode, LED4.cathode, R10.Pin_0, R11.Pin_1, LED-RGB-Starter1.connector1, LED-RGB-Starter1.connector3, R12.leg2
  N2: Arduino1.D11, S2.leg0, R11.Pin_0
  N3: Arduino1.D10, R10.Pin_1, S1.leg0
  N4: Arduino1.D9, R2.Pin_0
  N5: Arduino1.D8, R8.Pin_1
  N6: Arduino1.D7, R7.Pin_1
  N7: Arduino1.D6, R4.Pin_0
  N8: Arduino1.D5, R1.Pin_1
  N9: Arduino1.D4, R6.Pin_1
  N10: Arduino1.D3, R3.Pin_1
  N11: Arduino1.D2, R5.Pin_1
  N12: Arduino1.+5V, S2.leg1, S1.leg1, R12.leg1
  N13: Arduino1.A4, R12.wiper
  N14: R2.Pin_1, LED-RGB-Starter1.connector5
  N15: R3.Pin_0, LED-RGB-Starter1.connector2
  N16: R4.Pin_1, LED-RGB-Starter1.connector4
  N17: LED1.anode, R5.Pin_0
  N18: LED2.anode, R6.Pin_0
  N19: LED3.anode, R7.Pin_0
  N20: LED4.anode, R8.Pin_0
  N21: R1.Pin_0, LED-RGB-Starter1.connector0

notes:
  This is a colour mixer for the RGB LED of the Fritzing starter set. The RGB-LED part is a custom part which I modeled after how I put the part on the breadboard.
  The four single colour LEDs indicate which of the RGB colours is controlled by the potentiometer. There are two blue LEDs since the RGB LED has two blue anodes. As the starter kit does not provide blue LEDs, you might need to use the yellow ones for them.
  The left button selects the active colour. The right button activates the potentiometer for that colour.
