# Fritzing sketch id3432_RGB_LED_0 (saved by Fritzing 0.9.3b)
breadboards: 1

parts:
  LED1 = RGB LED (com. cathode, rgb) [package="5 mm [THT]"]
  Part1 = Arduino Uno (Rev3)
  R1 = Resistor [tolerance=±5% resistance=1k package=THT]
  R2 = Resistor [tolerance=±5% resistance=1k package=THT]
  R3 = Resistor [tolerance=±5% resistance=1k package=THT]

nets:
  N1: LED1.red_anode, R3.Pin_1
  N2: LED1.common_cathode, Part1.GND
  N3: LED1.green_anode, R2.Pin_1
  N4: LED1.blue_anode, R1.Pin_0
  N5: Part1.D9_PWM, R2.Pin_0
  N6: Part1.D10_PWM/SS, R1.Pin_1
  N7: Part1.D11_PWM/MOSI, R3.Pin_0
