# Fritzing sketch id3437_RGBledstrip_dimmer2_0 (saved by Fritzing 0.9.1b)
circuit board: 4.50966cm x 4.56863cm
breadboards: 1

parts:
  J3 = Screw terminal - 2 pins [package=THT]
  Arduino_Pro_Mini = Arduino Pro Mini v13
  SW = Pushbutton [package="[THT]"]
  R1 = Resistor [tolerance=±5% resistance=220 package=THT]
  R2 = Resistor [tolerance=±5% resistance=220 package=THT]
  Q1 = MOSFET-NCHANNEL [package=to220v]
  Q2 = MOSFET-NCHANNEL [package=to220v]
  Q3 = MOSFET-NCHANNEL [package=to220v]
  J4 = Screw terminal - 2 pins [package=THT]
  J5 = Screw terminal - 2 pins [package=THT]
  R3 = Resistor [tolerance=±5% resistance=220 package=THT]
  R4 = Resistor [tolerance=±5% resistance=220 package=THT]
  RF433_MHZ = RF-LINK_RX [package=rf-link_rx]
  ANT = Antenna

nets:
  N1: J3.pin1, Arduino_Pro_Mini.RAW, J4.pin2
  VCC: Arduino_Pro_Mini.VCC, SW.Pin_1, SW.Pin_2, RF433_MHZ.+5V
  N2: Arduino_Pro_Mini.D9_PWM, Q1.G, R3.Pin_0
  N3: Arduino_Pro_Mini.D6_PWM, R1.Pin_0, Q3.G
  N4: Arduino_Pro_Mini.D5_PWM, R2.Pin_0, Q2.G
  N5: Arduino_Pro_Mini.D3_PWM, RF433_MHZ.DATA
  N6: Arduino_Pro_Mini.D2, SW.Pin_3, SW.Pin_4, R4.Pin_1
  N7: Q1.D, J5.pin2
  N8: Q2.D, J5.pin1
  N9: Q3.D, J4.pin1
  N10: RF433_MHZ.ANT, ANT.antenna_lead
