# Fritzing sketch id3438_rgbwithcode_0 (saved by Fritzing 0.9.1b)
breadboards: 1

parts:
  Raspberry_Pi1 = Raspberry Pi B+
  LED1 = RGB LED (com. cathode, rgb) [package="5 mm [THT]"]

nets:
  N1: Raspberry_Pi1.GPIO19, LED1.green_anode
  N2: Raspberry_Pi1.GPIO26, LED1.blue_anode
  N3: Raspberry_Pi1.GND, LED1.common_cathode
