# Fritzing sketch id3440_rgblightnocode_0 (saved by Fritzing 0.9.1b)
breadboards: 1

parts:
  LED1 = RGB LED (com. cathode, rgb) [package="5 mm [THT]"]
  S1 = Pushbutton [package="[THT]"]
  R1 = Resistor [tolerance=±5% resistance=220 package=THT]
  S2 = Pushbutton [package="[THT]"]
  S3 = Pushbutton [package="[THT]"]
  Part1 = Arduino Uno (Rev3)
  Raspberry_Pi1 = Raspberry Pi B+

nets:
  N1: LED1.red_anode, S3.Pin_1, S3.Pin_2
  GND: LED1.common_cathode, Part1.GND, Raspberry_Pi1.GND
  N2: LED1.green_anode, S1.Pin_1, S1.Pin_2
  N3: LED1.blue_anode, S2.Pin_1, S2.Pin_2
  N4: S1.Pin_3, S1.Pin_4, S3.Pin_3, S3.Pin_4
  5V: R1.Pin_0, Part1.5V, Raspberry_Pi1.5V
  N5: S2.Pin_3, S2.Pin_4
