# Fritzing sketch id3441_test_0 (saved by Fritzing 0.8.0b)
breadboards: 2

parts:
  Composants1 = Arduino Uno (Rev3)
  IC1 = IC, DIP package, 28 pins [chip_label="TLC5940 1" part_number=IC1]
  IC2 = IC, DIP package, 28 pins [chip_label="TLC5940 2" part_number=IC2]
  R2 = Resistor [tolerance=±5% resistance=2.2k package=THT]
  R1 = Resistor [tolerance=±5% resistance=10k package=THT]
  R3 = Resistor [tolerance=±5% resistance=2.2k package=THT]
  U1 = 74HC595 [package="DIP16 [THT]"]
  IC3 = IC, DIP package, 18 pins [chip_label=UDN2981A]
  IC4 = IC, DIP package, 32 pins [chip_label=MATRICE_RGB_AC]

nets:
  5V: Composants1.5V, IC1.pin19, IC1.pin21, IC2.pin19, IC2.pin21, R1.Pin_0, U1.MR, U1.VCC, IC3.pin9
  GND: Composants1.GND, IC1.pin22, IC1.pin27, IC2.pin22, R2.Pin_0, R3.Pin_0, U1.GND, U1.OE, IC3.pin10
  N1: Composants1.D9_PWM, IC1.pin24, IC2.pin24
  N2: Composants1.D10_PWM/SS, IC1.pin23, IC2.pin23, R1.Pin_1
  N3: Composants1.D11_PWM/MOSI, IC1.pin26
  N4: Composants1.D13/SCK, IC1.pin25, IC2.pin25
  N5: Composants1.D3_PWM, IC1.pin18, IC2.pin18
  N6: Composants1.D4, U1.DS
  N7: Composants1.D5_PWM, U1.ST_CP
  N8: Composants1.D6_PWM, U1.SH_CP
  N9: IC1.pin1, IC4.pin15
  N10: IC1.pin2, IC4.pin14
  N11: IC1.pin3, IC4.pin13
  N12: IC1.pin4, IC4.pin12
  N13: IC1.pin5, IC4.pin11
  N14: IC1.pin6, IC4.pin10
  N15: IC1.pin7, IC4.pin9
  N16: IC1.pin8, IC4.pin8
  N17: IC1.pin9, IC4.pin7
  N18: IC1.pin10, IC4.pin6
  N19: IC1.pin11, IC4.pin5
  N20: IC1.pin12, IC4.pin4
  N21: IC1.pin13, IC4.pin3
  N22: IC1.pin14, IC4.pin2
  N23: IC1.pin15, IC4.pin1
  N24: IC1.pin17, IC2.pin26
  N25: IC1.pin20, R2.Pin_1
  N26: IC1.pin28, IC4.pin16
  N27: IC2.pin1, IC4.pin22
  N28: IC2.pin2, IC4.pin23
  N29: IC2.pin3, IC4.pin24
  N30: IC2.pin4, IC4.pin25
  N31: IC2.pin5, IC4.pin26
  N32: IC2.pin6, IC4.pin27
  N33: IC2.pin7, IC4.pin28
  N34: IC2.pin20, R3.Pin_1
  N35: IC2.pin28, IC4.pin21
  N36: U1.Q1, IC3.pin7
  N37: U1.Q2, IC3.pin6
  N38: U1.Q3, IC3.pin5
  N39: U1.Q4, IC3.pin4
  N40: U1.Q5, IC3.pin3
  N41: U1.Q6, IC3.pin2
  N42: U1.Q7, IC3.pin1
  N43: U1.Q0, IC3.pin8
  N44: IC3.pin11, IC4.pin32
  N45: IC3.pin12, IC4.pin31
  N46: IC3.pin13, IC4.pin30
  N47: IC3.pin14, IC4.pin29
  N48: IC3.pin15, IC4.pin20
  N49: IC3.pin16, IC4.pin19
  N50: IC3.pin17, IC4.pin18
  N51: IC3.pin18, IC4.pin17
