# Fritzing sketch id3442_LED_controller_0 (saved by Fritzing 0.9.3b)
circuit board: 8cm x 3.8cm
breadboards: 1

parts:
  Q1 = PNP-Transistor [package="TO92 [THT]"]
  Q2 = PNP-Transistor [package="TO92 [THT]"]
  Q3 = PNP-Transistor [package="TO92 [THT]"]
  Q4 = NPN-Transistor [package="TO92 [THT]"]
  ATTiny85 = attiny85 [package=dip]
  LED1 = RGB LED - (4 legs) [package="5 mm [THT]"]
  LED2 = RGB LED - (4 legs) [package="5 mm [THT]"]
  LED3 = RGB LED - (4 legs) [package="5 mm [THT]"]
  LED4 = RGB LED - (4 legs) [package="5 mm [THT]"]
  T_5V_G_3v3 = female pin header, 4 pins [form="♀ (female)"]
  Q5 = NPN-Transistor [package="TO92 [THT]"]
  D1 = Zener Diode [part_number=1N4732A breakdown_voltage=9.1V package="300 mil [THT]"]
  D2 = Zener Diode [part_number=1N4732A breakdown_voltage=9.1V package="300 mil [THT]"]
  D3 = Zener Diode [part_number=1N4732A breakdown_voltage=9.1V package="300 mil [THT]"]
  R4 = Resistor [tolerance=±5% resistance=1k package="1206 [SMD]"]
  R3 = Resistor [tolerance=±5% resistance=22k package="1206 [SMD]"]
  R2 = Resistor [tolerance=±5% resistance=100k package="1206 [SMD]"]
  R1 = Resistor [tolerance=±5% resistance=100k package="1206 [SMD]"]
  R5 = Resistor [tolerance=±5% resistance=2.2k package="1206 [SMD]"]

nets:
  N1: Q1.E, Q2.E, Q3.E, ATTiny85.Pin_8, T_5V_G_3v3.pin2
  N2: Q1.B, R1.Pin_1
  N3: Q1.C, LED1.blue_cathode, LED2.blue_cathode, LED3.blue_cathode, LED4.blue_cathode
  N4: Q2.B, R2.Pin_1
  N5: Q2.C, LED1.green_cathode, LED2.green_cathode, LED3.green_cathode, LED4.green_cathode, Q5.C
  N6: Q3.B, R3.Pin_0
  N7: Q3.C, LED1.red_cathode, LED2.red_cathode, LED3.red_cathode, LED4.red_cathode
  N8: Q4.E, ATTiny85.Pin_2
  N9: Q4.B, R5.Pin_0
  N10: Q4.C, ATTiny85.Pin_4, T_5V_G_3v3.pin3, Q5.E
  N11: ATTiny85.Pin_5, D2.anode, R1.Pin_0
  N12: ATTiny85.Pin_6, D3.anode, R2.Pin_0
  N13: ATTiny85.Pin_7, D1.anode, R3.Pin_1
  N14: LED1.common_anode, LED2.common_anode, LED3.common_anode, LED4.common_anode
  N15: T_5V_G_3v3.pin1, R5.Pin_1
  N16: Q5.B, R4.Pin_1
  N17: D1.cathode, D2.cathode, D3.cathode, R4.Pin_0
