# Fritzing sketch id3443_rgb_seq_0 (saved by Fritzing 0.7.4b)
breadboards: 1

parts:
  Arduino1 = Arduino
  RE1 = Rotary Encoder [package=THT]
  S1 = Pushbutton [package="[THT]"]
  S2 = Pushbutton [package="[THT]"]
  S3 = Pushbutton [package="[THT]"]
  LED1 = RGB LED (com. cathode, rbg) [package="5 mm [THT]"]
  R5 = Resistor [tolerance=±5% resistance=10k package=THT]
  R6 = Resistor [tolerance=±5% resistance=10k package=THT]
  R7 = Resistor [tolerance=±5% resistance=10k package=THT]
  R8 = Resistor [tolerance=±5% resistance=330 package=THT]
  R9 = Resistor [tolerance=±5% resistance=330 package=THT]
  R10 = Resistor [tolerance=±5% resistance=330 package=THT]
  LED2 = LED - 5mm [color="Red (633nm)" package="5 mm [THT]"]
  R11 = Resistor [tolerance=±5% resistance=330 package=THT]

nets:
  N1: Arduino1.D11, R10.Pin_1
  N2: Arduino1.D10, R9.Pin_1
  N3: Arduino1.D9, R8.Pin_1
  N4: Arduino1.D5, R11.Pin_1
  N5: Arduino1.D4, Arduino1.D3, Arduino1.D2, Arduino1.GND, RE1.EncoderPinB, S1.Pin_1, S1.Pin_2, S2.Pin_1, S2.Pin_2, S3.Pin_1, S3.Pin_2, LED2.anode
  N6: Arduino1.+5V, RE1.EncoderPinA, S3.Pin_3, S3.Pin_4, LED1.common_cathode, R5.Pin_1, R6.Pin_1, R7.Pin_0, R7.Pin_1
  N7: Arduino1.A0, RE1.EncoderPinC
  N8: S1.Pin_3, S1.Pin_4, R5.Pin_0
  N9: S2.Pin_3, S2.Pin_4, R6.Pin_0
  N10: LED1.red_anode, R8.Pin_0
  N11: LED1.blue_anode, R9.Pin_0
  N12: LED1.green_anode, R10.Pin_0
  N13: LED2.cathode, R11.Pin_0
