# Fritzing sketch id3444_RGB_Streetlight_0 (saved by Fritzing 0.9.3b)
breadboards: 1

parts:
  Part1 = Arduino Uno (Rev3)
  R1 = Photocell (LDR) [package=THT]
  LED1 = RGB LED (com. cathode, rgb) [package="5 mm [THT]"]
  R2 = Resistor [tolerance=±5% resistance=220 package=THT]
  R3 = Rotary Potentiometer (Small) [maximum_resistance=100kΩ package=THT]
  R4 = Rotary Potentiometer (Small) [maximum_resistance=100kΩ package=THT]
  R5 = Rotary Potentiometer (Small) [maximum_resistance=100kΩ package=THT]
  R6 = Resistor [tolerance=±5% resistance=220 package=THT]
  R7 = Resistor [tolerance=±5% resistance=220 package=THT]
  R8 = Resistor [tolerance=±5% resistance=220 package=THT]
  LED2 = LED - 5mm [color="Red (633nm)" package="5 mm [THT]"]
  R9 = Resistor [tolerance=±5% resistance=220 package=THT]

nets:
  N1: Part1.A1, R1.pin_0
  N2: Part1.A2, R3.wiper
  N3: Part1.A3, R4.wiper
  N4: Part1.A4/SDA, R5.wiper
  N5: Part1.D9_PWM, R8.Pin_1
  N6: Part1.D10_PWM/SS, R7.Pin_1
  N7: Part1.D11_PWM/MOSI, R6.Pin_1
  N8: Part1.D12/MISO, LED2.anode
  N9: Part1.5V, R3.leg2, R4.leg2, R5.leg2
  N10: Part1.GND, LED1.common_cathode, R2.Pin_1, R3.leg1, R4.leg1, R5.leg1, R9.Pin_0
  N11: R1.pin_1, R2.Pin_0
  N12: LED1.red_anode, R6.Pin_0
  N13: LED1.green_anode, R7.Pin_0
  N14: LED1.blue_anode, R8.Pin_0
  N15: LED2.cathode, R9.Pin_1
