# Fritzing sketch id3445_1642d318fc8a872dda2bf512ecc49bc8_copy (saved by Fritzing 0.9.2b)
breadboards: 1

parts:
  J1 = Basic Servo
  J2 = Basic Servo
  J3 = Basic Servo
  J4 = Basic Servo
  Part1 = Arduino Uno (Rev3)
  BAT1 = BC9VPC [package=bc9vpc]

nets:
  GND: J1.gnd, J2.gnd, J3.gnd, J4.gnd, BAT1.V+
  VCC: J1.vcc, J2.vcc, J3.vcc, J4.vcc, BAT1.V-
  N1: J1.pulse, Part1.D8
  N2: J2.pulse, Part1.D9_PWM
  N3: J3.pulse, Part1.D10_PWM/SS
  N4: J4.pulse, Part1.D11_PWM/MOSI
