# Fritzing sketch id3449_rgbstripe_mit_5buttons_0 (saved by Fritzing 0.7.9b)
breadboards: 1

parts:
  FET-B = STP16NF06_N_Channel_Power_MOSFET
  FET-G = STP16NF06_N_Channel_Power_MOSFET
  FET-R = STP16NF06_N_Channel_Power_MOSFET
  PWR_12V = Screw terminal - 2 pins [package=THT]
  +_R = Screw terminal - 2 pins [package=THT]
  G_B = Screw terminal - 2 pins [package=THT]
  StripeShield = Arduino
  S1 = Pushbutton [package="[THT]"]
  S2 = Pushbutton [package="[THT]"]
  S3 = Pushbutton [package="[THT]"]
  S4 = Pushbutton [package="[THT]"]
  S5 = Pushbutton [package="[THT]"]

nets:
  N1: FET-B.connector1, StripeShield.D11
  N2: FET-B.connector2, G_B.pin2
  N3: FET-B.connector3, FET-G.connector3, FET-R.connector3, PWR_12V.pin1, StripeShield.GND, S1.Pin_3, S1.Pin_4, S2.Pin_3, S2.Pin_4, S3.Pin_3, S3.Pin_4, S4.Pin_3, S4.Pin_4, S5.Pin_3, S5.Pin_4
  N4: FET-G.connector1, StripeShield.D10
  N5: FET-G.connector2, G_B.pin1
  N6: FET-R.connector1, StripeShield.D9
  N7: FET-R.connector2, +_R.pin2
  N8: PWR_12V.pin2, +_R.pin1
  N9: StripeShield.D6, S5.Pin_1, S5.Pin_2
  N10: StripeShield.D5, S4.Pin_1, S4.Pin_2
  N11: StripeShield.D4, S3.Pin_1, S3.Pin_2
  N12: StripeShield.D3, S2.Pin_1, S2.Pin_2
  N13: StripeShield.D2, S1.Pin_1, S1.Pin_2
