# Fritzing sketch id344_Atari_Punk_Console_0 (saved by Fritzing 0.9.0b)
circuit board: 7.2cm x 5.64444cm
breadboards: 1

parts:
  IC2 = IC, DIP package, 14 pins [chip_label=556]
  Power = Power plug
  R2 = Resistor [tolerance=±5% resistance=1k package=THT]
  D1 = LED - 5mm [color="Red (633nm)" package="5 mm [THT]"]
  C5 = Electrolytic Capacitor [capacitance=10µF package="100 mil [THT, electrolytic]"]
  SW1 = Toggle Switch [package=THT]
  C4 = Ceramic Capacitor [capacitance=100nF package="100 mil [THT, multilayer]"]
  C2 = Ceramic Capacitor [capacitance=100nF package="100 mil [THT, multilayer]"]
  R1 = Resistor [tolerance=±5% resistance=1k package=THT]
  VR2 = Rotary Potentiometer (Small) [maximum_resistance=500kΩ package=THT]
  VR3 = Rotary Potentiometer (Small) [maximum_resistance=500kΩ package=THT]
  C3 = Electrolytic Capacitor [capacitance=10µF package="100 mil [THT, electrolytic]"]
  R3 = Resistor [tolerance=±5% resistance=4.7k package=THT]
  Headphones = Audio Jack (TRS) 3.5mm [package="4Ucon 08780 [THT]"]
  R4 = Resistor [tolerance=±5% resistance=10k package=THT]
  CV(A) = Audio Jack (TRS) 3.5mm [package="4Ucon 08780 [THT]"]
  CV(B) = Audio Jack (TRS) 3.5mm [package="4Ucon 08780 [THT]"]
  D2 = Rectifier Diode [part_number=1N4001 package="300 mil [THT]"]
  VR1 = Rotary Potentiometer (Small) [maximum_resistance=100kΩ package=THT]
  C1 = Ceramic Capacitor [capacitance=10nF package="100 mil [THT, multilayer]"]

nets:
  N1: IC2.pin1, R1.Pin_0, VR2.leg1, VR2.wiper
  N2: IC2.pin2, IC2.pin6, R1.Pin_1, C1.1
  N3: IC2.pin3, CV(B).Tip
  N4: IC2.pin4, IC2.pin10, IC2.pin14, VR2.leg2, VR3.leg2, D2.cathode
  N5: IC2.pin5, IC2.pin8
  N6: IC2.pin7, Power.GND, D1.anode, C5.-, C4.1, C2.1, R3.Pin_0, Headphones.Sleeve, CV(A).Sleeve, CV(B).Sleeve, VR1.leg2, C1.0
  N7: IC2.pin9, C3.+
  N8: IC2.pin11, CV(A).Tip
  N9: IC2.pin12, IC2.pin13, C2.0, VR3.leg1, VR3.wiper
  N10: Power.VCC, SW1.COM
  N11: R2.Pin_0, C5.+, SW1.L1, C4.0, D2.anode
  N12: R2.Pin_1, D1.cathode
  N13: C3.-, R4.Pin_0
  N14: R3.Pin_1, R4.Pin_1, VR1.leg1
  N15: Headphones.Tip, VR1.wiper

notes:
  APC w/ CV inputs
  rcj4747
