# Fritzing sketch id3451_RGB3potColorMixer_by_Uaneme_1_0 (saved by Fritzing 0.9.2b)
breadboards: 2

parts:
  R1 = Rotary Potentiometer (Large) [maximum_resistance=100kΩ package=THT]
  R2 = Rotary Potentiometer (Large) [maximum_resistance=100kΩ package=THT]
  R3 = Rotary Potentiometer (Large) [maximum_resistance=100kΩ package=THT]
  Part1 = Arduino Nano (Rev3.0)
  Part2 = ws2812b [package="smd 2812b"]
  Part3 = ws2812b [package="smd 2812b"]
  Part4 = ws2812b [package="smd 2812b"]
  Part5 = ws2812b [package="smd 2812b"]
  Part6 = ws2812b [package="smd 2812b"]
  Part7 = ws2812b [package="smd 2812b"]
  Part8 = ws2812b [package="smd 2812b"]
  Part9 = ws2812b [package="smd 2812b"]

nets:
  VDD: R1.leg1, R2.leg1, R3.leg1, Part1.5V, Part2.VDD, Part3.VDD, Part4.VDD, Part5.VDD, Part6.VDD, Part7.VDD, Part8.VDD, Part9.VDD
  N1: R1.wiper, Part1.A0
  VSS: R1.leg2, R2.leg2, R3.leg2, Part1.GND, Part2.VSS, Part3.VSS, Part4.VSS, Part5.VSS, Part6.VSS, Part7.VSS, Part8.VSS, Part9.VSS
  N2: R2.wiper, Part1.A2
  N3: R3.wiper, Part1.A4
  N4: Part1.D11/MOSI, Part2.DIN
  N5: Part2.DOUT, Part3.DIN
  N6: Part4.DOUT, Part5.DIN
  N7: Part5.DOUT, Part6.DIN
  N8: Part6.DOUT, Part7.DIN
  N9: Part7.DOUT, Part8.DIN
  N10: Part8.DOUT, Part9.DIN
