# Fritzing sketch id3453_rgb_led_0 (saved by Fritzing 0.9.2b)
breadboards: 1

parts:
  LED1 = RGB LED (com. cathode, rbg) [package="5 mm [THT]"]
  Composant1 = Arduino Uno (Rev3)
  R1 = Resistor [tolerance=±5% resistance=220 package=THT]
  R2 = Resistor [tolerance=±5% resistance=220 package=THT]
  R3 = Resistor [tolerance=±5% resistance=220 package=THT]

nets:
  N1: LED1.red_anode, R1.Pin_1
  N2: LED1.common_cathode, Composant1.GND
  N3: LED1.blue_anode, R2.Pin_1
  N4: LED1.green_anode, R3.Pin_1
  N5: Composant1.D9_PWM, R3.Pin_0
  N6: Composant1.D10_PWM/SS, R2.Pin_0
  N7: Composant1.D11_PWM/MOSI, R1.Pin_0
