# Fritzing sketch id3454_RGB_infrarossi_0 (saved by Fritzing 0.9.1b)
breadboards: 1

parts:
  LED1 = RGB LED (com. cathode, rgb) [package="5 mm [THT]"]
  Componente1 = Arduino Mega 2560 (Rev3)
  R1 = Resistor [tolerance=±5% resistance=220 package=THT]
  R2 = Resistor [tolerance=±5% resistance=220 package=THT]
  R3 = Resistor [tolerance=±5% resistance=220 package=THT]
  IR1 = TSOP312.., 314.. [package=THT]

nets:
  N1: LED1.red_anode, R3.Pin_0
  GND: LED1.common_cathode, Componente1.GND, IR1.GND
  N2: LED1.green_anode, R2.Pin_0
  N3: LED1.blue_anode, R1.Pin_0
  N4: Componente1.D11_PWM, IR1.Vs
  N5: Componente1.D8_PWM, R3.Pin_1
  N6: Componente1.5V, IR1.Data
  N7: Componente1.D2_PWM, R1.Pin_1
  N8: Componente1.D4_PWM, R2.Pin_1
