# Fritzing sketch id3455_RHT03HumiditySensor_0 (saved by Fritzing 0.9.3b)
breadboards: 1

parts:
  Part1 = Arduino Uno (Rev3)
  RHT1 = Humidity and Temperature Sensor RHT03
  R1_1K_Ohm = 1K Ohm resistor

nets:
  N1: Part1.D7, RHT1.Data-signal, R1_1K_Ohm.connector1
  3V3: Part1.3V3, RHT1.Vcc, R1_1K_Ohm.connector0
  N2: Part1.GND, RHT1.GND_2

notes:
  Pin 1: to Vcc: 3.3v
  Pin 2: Data Signal; to digital pin of choice.
  Pin 3: NOT USED: NULL
  Pin 4: to GND (ground)
