# Fritzing sketch id3456_RIB_Programmer_0 (saved by Fritzing 0.9.2b)
circuit board: 5.09984cm x 3.1783cm
breadboards: 1

parts:
  78L05 = prefix0000 [part_number=78L05]
  1uF = Electrolytic Capacitor [capacitance=1µF voltage=16V package="100 mil [THT, electrolytic]"]
  12V_- = Screw terminal - 2 pins [package=THT]
  U2 = RS232 Transceiver [package=dil16]
  Serial = DB9 Connector [package=db9]
  1uF_2 = Electrolytic Capacitor [capacitance=1µF voltage=16V package="100 mil [THT, electrolytic]"]
  1uF_3 = Electrolytic Capacitor [capacitance=1µF voltage=16V package="100 mil [THT, electrolytic]"]
  1uF_4 = Electrolytic Capacitor [capacitance=1µF voltage=16V package="100 mil [THT, electrolytic]"]
  1uF_5 = Electrolytic Capacitor [capacitance=1µF voltage=16V package="100 mil [THT, electrolytic]"]
  0_01uF = Capacitor [part_number=0.01uF package=cap-pth-small2]
  RXTX+VGND = male pin header, 4 pins [form="♂ (male)"]

nets:
  N1: 78L05.connector0, 12V_-.pin2, 0_01uF.1, RXTX+VGND.pin2
  N2: 78L05.connector1, 1uF.-, 12V_-.pin1, U2.GND, 0_01uF.2, RXTX+VGND.pin1
  N3: 78L05.connector2, 1uF.+, U2.VCC, 1uF_4.-
  N4: U2.C1+, 1uF_2.+
  N5: U2.V+, 1uF_4.+
  N6: U2.C1-, 1uF_2.-
  N7: U2.C2+, 1uF_3.+
  N8: U2.C2-, 1uF_3.-
  N9: U2.V-, 1uF_5.+
  N10: U2.T2OUT, Serial.2
  N11: U2.R2IN, Serial.3
  N12: U2.R2OUT, RXTX+VGND.pin4
  N13: U2.T2IN, RXTX+VGND.pin3
  N14: Serial.4, Serial.6
  N15: Serial.5, 1uF_5.-
  N16: Serial.7, Serial.8

notes:
  RIB Programmer
