# Fritzing sketch id3457_Nuevo_FRITZ_0 (saved by Fritzing 0.9.3b)
breadboards: 1

parts:
  Componente1 = Arduino Mega 2560 (Rev3)
  LED3 = LED - 5mm [color="Red (633nm)" package="5 mm [THT]"]
  LED4 = LED - 5mm [color="Green (570nm)" package="5 mm [THT]"]
  R3 = Resistor [tolerance=±5% resistance=220 package=THT]
  R4 = Resistor [tolerance=±5% resistance=220 package=THT]

nets:
  N1: Componente1.D13_PWM, LED3.anode
  N2: Componente1.D10_PWM, LED4.anode
  N3: Componente1.GND, R3.Pin_1, R4.Pin_1
  N4: LED3.cathode, R3.Pin_0
  N5: LED4.cathode, R4.Pin_0
