# Fritzing sketch id3458_Schematic_0 (saved by Fritzing 0.9.2b)
breadboards: 1

parts:
  Part1 = Triple Axis Accelerometer Breakout - ADXL335
  V1 = DC Power [voltage=5]
  Part3 = Arduino Micro (Rev3)
  Part5 = Bluetooth Mate Silver

nets:
  N1: Part1.YOUT, Part3.A1
  N2: Part1.XOUT, Part3.A0
  GND: Part1.GND, Part3.GND, Part5.GND
  VCC: Part1.VCC, V1.V+, Part5.VCC
  N3: V1.V-, Part3.5V
  N4: Part3.D1/TX, Part5.TX_5V
  N5: Part3.D0/RX, Part5.RX_5V
