# Fritzing sketch id3460_RITA_Sketch_embDe9V_0 (saved by Fritzing 0.9.3b)
breadboards: 1

parts:
  R1 = Resistor [tolerance=±5% resistance=220 package=THT]
  LED1 = LED - 5mm [color="Red (633nm)" package="5 mm [THT]"]
  LED2 = LED - 5mm [color="Green (570nm)" package="5 mm [THT]"]
  R2 = Resistor [tolerance=±5% resistance=220 package=THT]
  Componente1 = Arduino Mega ADK (Rev3)

nets:
  N1: R1.Pin_0, LED2.anode
  N2: R1.Pin_1, R2.Pin_1, Componente1.RESET
  N3: LED1.cathode, Componente1.D13_PWM
  N4: LED1.anode, R2.Pin_0
  N5: LED2.cathode, Componente1.D11_PWM
