# Fritzing sketch id3461_RNG_Sketch_1_0 (saved by Fritzing 0.9.2b)
breadboards: 1

parts:
  R1 = Resistor [tolerance=±5% resistance=1M package=THT]
  R2 = Resistor [tolerance=±5% resistance=4.7k package=THT]
  C1 = Tantalum Capacitor [capacitance=1μF package="100 mil [THT, tantalum]"]
  Q1 = NPN-Transistor [package="TO92 [THT]"]
  Q2 = NPN-Transistor [package="TO92 [THT]"]
  Q3 = NPN-Transistor [package="TO92 [THT]"]
  R3 = Resistor [tolerance=±5% resistance=10k package=THT]
  C2 = Electrolytic Capacitor [capacitance=10µF package="0807 [SMD, electrolytic]"]
  R4 = Resistor [tolerance=±5% resistance=4.7k package=THT]

nets (from the pcb view):
  N1: R1.Pin_0, C1.-, Q1.E, Q2.C
  N2: R1.Pin_1, R2.Pin_1, R3.Pin_0, C2.+
  N3: R2.Pin_0, C1.+, Q3.B
  N4: Q1.B, Q2.B
  N5: Q2.E, Q3.E, Q3.C, R3.Pin_1, C2.-, R4.Pin_0, R4.Pin_1
