# Fritzing sketch id3463_NRF24L01_ARDUINOMEGA_0 (saved by Fritzing 0.9.2b)

parts:
  NRF24L1 = NRF24L01
  Componente4 = Arduino Mega 2560 (Rev3)

nets:
  N1: NRF24L1.connector0, Componente4.3V3
  N2: NRF24L1.connector1, Componente4.D10_PWM
  N3: NRF24L1.connector2, Componente4.D51
  N4: NRF24L1.connector4, Componente4.GND
  N5: NRF24L1.connector5, Componente4.D9_PWM
  N6: NRF24L1.connector6, Componente4.D52
  N7: NRF24L1.connector7, Componente4.D50

notes:
  GND = Preto (Pino 1)
  VCC = Laranja (Pino 2)
  CE = Azul (Pino 9)
  CSN = Amarelo (Pino 10)
  SCK = Cinza (Pino 52)
  MOSI = Lilás (Pino 51)
  MISO = Ciano (Pino 50)
  IRQ = Não Conectado
  NRF24L01, utilizado para comunicação com o outro módulo conectado ao Joystick Shield
  Arduino MEGA could be unstable on
  3.3 V output, so you have some problem , try to correct the ripple placing a 10uF capacitor.
  Usefull information on:
  http://arduino-info.wikispaces.com/Nrf24L01-2.4GHz-HowTo
