# Fritzing sketch id3464_RFID_Display_0 (saved by Fritzing 0.9.2b)
circuit board: 8.46667cm x 5.64444cm
breadboards: 1

parts:
  U1 = LCD-16X2 [package=lcd-16x2]
  R1 = Trimmer Potentiometer [maximum_resistance=10kΩ package=THT]
  Bauteil1 = Arduino Uno (Rev3)
  R2 = Resistor [tolerance=±5% resistance=220 package=THT]
  U2 = 2.4GHz Low Power Transceiver [package=qfn20]  # not connected

nets:
  VSS: U1.VSS, U1.R_W, U1.K, R1.leg2, Bauteil1.GND
  VDD: U1.VDD, R1.leg1, Bauteil1.5V, R2.Pin_0
  N1: U1.VO, R1.wiper
  N2: U1.RS, Bauteil1.D7
  N3: U1.E, Bauteil1.D6_PWM
  N4: U1.DB4, Bauteil1.D5_PWM
  N5: U1.DB5, Bauteil1.D4
  N6: U1.DB6, Bauteil1.D3_PWM
  N7: U1.DB7, Bauteil1.D2
  N8: U1.A, R2.Pin_1
