# Fritzing sketch id3467_Robo_Presenter_Uno_Buildout_0 (saved by Fritzing 0.8.7b)
circuit board: 2.3cm x 2.3cm
breadboards: 1

parts:
  Part1 = Arduino Uno (Rev3)
  U2 = RELAY-2 [package=relay-g5v]
  LED1 = LED - 3mm [color="Green (560nm)" package="3 mm [THT]"]
  R1 = Resistor [tolerance=±5% resistance=150 package=THT]
  D1 = Diode [package=diode-1n4148]
  D2 = Diode [package=diode-1n4148]
  L1 = Solenoid
  L2 = Solenoid
  V1 = DC Power [voltage=12V]
  IR1 = TSOP312.., 314.. [package=THT]
  D5 = Rectifier Diode [part_number=1N4001 package="300 mil [THT]"]
  D6 = Rectifier Diode [part_number=1N4001 package="300 mil [THT]"]
  U1 = RELAY-2 [package=relay-g5v]

nets:
  N1: Part1.D9_PWM, D6.anode
  N2: Part1.D10_PWM/SS, D5.anode
  N3: Part1.D13/SCK, LED1.anode
  GND: Part1.GND, R1.Pin_1, D1.C, D2.C, L1.pin1, L2.pin1, V1.V-, IR1.GND
  N4: Part1.D5_PWM, IR1.Data
  N5: Part1.5V, IR1.Vs
  N6: Part1.VIN, U2.5, V1.V+, U1.5
  N7: U2.2, D2.A
  N8: U2.9, D6.cathode
  N9: U2.10, L2.pin2
  N10: LED1.cathode, R1.Pin_0
  N11: D1.A, U1.2
  N12: L1.pin2, U1.10
  N13: D5.cathode, U1.9
