# Fritzing sketch id3468_Biped1_0 (saved by Fritzing 0.7.11b)
breadboards: 1

parts:
  Arduino1 = Arduino
  J1 = Basic Servo
  J2 = Basic Servo
  J3 = Basic Servo
  J4 = Basic Servo
  VCC1 = 4 x AAA Battery Mount

nets:
  N1: Arduino1.D6, J4.pulse
  N2: Arduino1.D5, J3.pulse
  N3: Arduino1.D4, J2.pulse
  N4: Arduino1.D3, J1.pulse
  GND: Arduino1.GND, J1.gnd, J2.gnd, J3.gnd, J4.gnd, VCC1.-
  VCC: J1.vcc, J2.vcc, J3.vcc, J4.vcc, VCC1.+
