# Fritzing sketch id3469_Wiring_Setup_0 (saved by Fritzing 0.9.3b)
breadboards: 1

parts:
  Part1 = Arduino Uno (Rev3)
  Part2 = Bluetooth HC-05 Macho
  M1 = DC Motor
  M2 = DC Motor
  Q1 = Basic FET N-Channel [package="TO220 [THT]"]
  Q2 = Basic FET N-Channel [package="TO220 [THT]"]
  LED1 = LED - 3mm [color="Yellow (595nm)" package="3 mm [THT]"]
  LED2 = LED - 3mm [color="Yellow (595nm)" package="3 mm [THT]"]  # not connected
  BAT1 = BC9VPC [package=bc9vpc]
  VCC1 = Battery block 9V  # not connected

nets:
  N1: Part1.D8, Q2.gate
  N2: Part1.D0/RX, Part2.TXD
  N3: Part1.D1/TX, Part2.RXD
  N4: Part1.D7, Q1.gate
  5V: Part1.5V, Part2.VCC, LED1.cathode, BAT1.V-
  GND: Part1.GND, Part2.GND, Q1.source, Q2.source
  N5: M1.pin_1, Q1.drain
  N6: M1.pin_2, M2.pin_1, LED1.anode, BAT1.V+
  N7: M2.pin_2, Q2.drain
