# Fritzing sketch id3470_robokitty_0 (saved by Fritzing 0.9.2b)
breadboards: 1

parts:
  Part1 = Photon
  BATT1 = 4xAA_Switchable_Battery_Pack_w_Bare_Wire
  J1 = Basic Servo

nets:
  N1: Part1.D0, J1.pulse
  N2: BATT1.connector1, J1.vcc
  N3: BATT1.connector2, J1.gnd
