# Fritzing sketch id3471_Roboknight_JTAG_Adapter_v1_0_0 (saved by Fritzing 0.8.3b)
circuit board: 4.23181cm x 4.57136cm

parts:
  ARM-20_JTAG = shrouded pin header, 20 pins [form="♂ (shrouded male)"]
  Systronix_JTAG = shrouded pin header, 10 pins [form="♂ (shrouded male)"]
  SB6141_JTAG = double row smd male pin header, 14 pins [form="♂ (male)"]

nets:
  N1: ARM-20_JTAG.pin1, ARM-20_JTAG.pin20, Systronix_JTAG.pin8, SB6141_JTAG.pin3
  N2: ARM-20_JTAG.pin2, Systronix_JTAG.pin5, SB6141_JTAG.pin14
  N3: ARM-20_JTAG.pin3, Systronix_JTAG.pin3, SB6141_JTAG.pin2
  N4: ARM-20_JTAG.pin4, Systronix_JTAG.pin2, SB6141_JTAG.pin1
  N5: ARM-20_JTAG.pin5, Systronix_JTAG.pin1, SB6141_JTAG.pin6
  N6: ARM-20_JTAG.pin6, SB6141_JTAG.pin5
  N7: ARM-20_JTAG.pin7, Systronix_JTAG.pin4, SB6141_JTAG.pin4
  N8: ARM-20_JTAG.pin9, SB6141_JTAG.pin7
  N9: ARM-20_JTAG.pin10, SB6141_JTAG.pin8
  GND: ARM-20_JTAG.pin11, ARM-20_JTAG.pin12, ARM-20_JTAG.pin13, ARM-20_JTAG.pin14, ARM-20_JTAG.pin15, ARM-20_JTAG.pin16, ARM-20_JTAG.pin17, ARM-20_JTAG.pin18, ARM-20_JTAG.pin19, Systronix_JTAG.pin6, Systronix_JTAG.pin7, Systronix_JTAG.pin9, Systronix_JTAG.pin10, SB6141_JTAG.pin9, SB6141_JTAG.pin10, SB6141_JTAG.pin11

notes:
  TRST
  TDI
  TMS
  RESET
  VCC
  TCK
  JTAG Adapter v1.1
  Roboknight
