# Fritzing sketch id3472_Robot_Arduino_Scratch_S4A_Map_0 (saved by Fritzing 0.7.11b)
breadboards: 1

parts:
  Arduino1 = Arduino
  Interruptor_ON-OFF = Toggle Switch [package=THT]
  LED1 = LED - 5mm [color="Red (633nm)" package="5 mm [THT]"]
  J1 = Basic Servo
  J2 = Basic Servo
  J3 = Piezo Speaker

nets:
  N1: Arduino1.GND, LED1.anode, J3.pin1
  N2: Arduino1.D13, LED1.cathode
  N3: Arduino1.D10, J3.pin2
  N4: Arduino1.D8, J1.pulse
  N5: Arduino1.D7, J2.pulse
  VCC: Interruptor_ON-OFF.L2, J1.vcc, J2.vcc
  GND: J1.gnd, J2.gnd

notes:
  Esquema Robot Arduino Scratch S4A Map
  Servo 2 Dirección
  Servo 1 Motor
