# Fritzing sketch id3473_Robot_Arduino_Minibloq_0 (saved by Fritzing 0.7.11b)
breadboards: 1

parts:
  Arduino1 = Arduino
  Interruptor_ON-OFF = Toggle Switch [package=THT]
  LED1 = LED - 5mm [color="Red (633nm)" package="5 mm [THT]"]
  Resistencia_10KOhm = Resistor [tolerance=±5% resistance=100k package=THT]
  Sensor_Inclinación = Tilt Switch [package=THT]
  J1 = Basic Servo
  J2 = Basic Servo

nets:
  N1: Arduino1.GND, LED1.anode
  N2: Arduino1.D13, LED1.cathode
  N3: Arduino1.D7, J1.pulse
  N4: Arduino1.D6, J2.pulse
  N5: Arduino1.D2, Resistencia_10KOhm.Pin_1, Sensor_Inclinación.Pin_1
  VCC: Interruptor_ON-OFF.L2, Sensor_Inclinación.Pin_2, J1.vcc, J2.vcc
  GND: J1.gnd, J2.gnd

notes:
  Esquema Robot Arduino Minibloq
