# Fritzing sketch id3475_Robot_Arduino_Physical_Etoys_SigueLinea_0 (saved by Fritzing 0.7.11b)
breadboards: 1

parts:
  Arduino1 = Arduino
  LED1 = LED - 5mm [color="Red (633nm)" package="5 mm [THT]"]
  S1 = Tilt Switch [package=THT]
  S2 = Tilt Switch [package=THT]
  R1 = Photocell (LDR) [package=THT]
  R2 = Photocell (LDR) [package=THT]
  R5 = Resistor [resistance=10k tolerance=±5% package=THT]
  R6 = Resistor [resistance=10k tolerance=±5% package=THT]
  J1 = Basic Servo
  J2 = Basic Servo
  S3 = Toggle Switch [package=THT]
  R7 = Resistor [resistance=220 tolerance=±5% package=THT]
  LED2 = LED - 5mm [color="Red (633nm)" package="5 mm [THT]"]
  R8 = Resistor [resistance=220 tolerance=±5% package=THT]
  LED3 = LED - 5mm [color="Red (633nm)" package="5 mm [THT]"]

nets:
  GND: Arduino1.GND, LED1.cathode, R1.pin_0, J1.gnd, S3.L1, LED2.anode, LED3.anode
  N1: Arduino1.D13, LED1.anode
  N2: Arduino1.D12, S1.Pin_2
  N3: Arduino1.D8, S2.Pin_2
  N4: Arduino1.D6, J1.pulse
  N5: Arduino1.D5, J2.pulse
  N6: Arduino1.+5V, S1.Pin_1, S2.Pin_1, R5.Pin_1, R6.Pin_1, S3.L2, R7.Pin_0, R8.Pin_0
  N7: Arduino1.A1, R1.pin_1, R6.Pin_0
  N8: Arduino1.A5, R2.pin_0, R5.Pin_0
  VCC: J1.vcc, J2.vcc
  N9: R7.Pin_1, LED2.cathode
  N10: R8.Pin_1, LED3.cathode

notes:
  Robot Arduino Physical Etoys Sigue Linea
  Sensor choque Derecha
  Sensor choque Izquierda
  LDR Derecha
  LDR Izquierda
  Servo Izquierda
  Servo Derecha
