# Fritzing sketch id3476_RobotKar2szervoval_2_0 (saved by Fritzing 0.7.4b)
breadboards: 1

parts:
  J1 = Basic Servo
  R1 = Rotary Potentiometer (Large) [maximum_resistance=1kΩ package=THT]
  Arduino2 = Arduino
  R2 = Rotary Potentiometer (Large) [maximum_resistance=1kΩ package=THT]
  J2 = Basic Servo
  L1 = Solenoid
  K1 = Relay [part_number=FRS1B-S package=THT]
  D1 = Rectifier Diode [part_number=1N4001 package="300 mil [THT]"]
  Q1 = NPN-Transistor [package="TO92 [THT]"]
  R3 = Resistor [tolerance=±5% resistance=1k package=THT]
  Power_plug1 = Power plug
  S1 = Toggle Switch [package=THT]

nets:
  GND: J1.gnd, R1.leg2, Arduino2.GND, R2.leg2, J2.gnd, Q1.E
  VCC: J1.vcc, R1.leg1, Arduino2.+5V, R2.leg1, J2.vcc, K1.COIL1, D1.cathode, S1.L1
  N1: J1.pulse, Arduino2.D9
  N2: R1.wiper, Arduino2.A5
  N3: Arduino2.D10, J2.pulse
  N4: Arduino2.D4, S1.COM
  N5: Arduino2.D2, R3.Pin_1
  N6: Arduino2.A0, R2.wiper
  N7: L1.pin1, Power_plug1.GND
  N8: L1.pin2, K1.B
  N9: K1.C1, K1.C2, Power_plug1.VCC
  N10: K1.COIL2, D1.anode, Q1.C
  N11: Q1.B, R3.Pin_0

notes:
  In this example, two potentiometer values are read in through two 'Analog In' pin. The values are then used to control the position of two servo motors.
  Or, the servos can be programmed.
  The button state determines which control works: the one with two potentiometers or a program itself.
  Related examples:
  http://arduino.cc/en/Tutorial/AnalogInput
  http://arduino.cc/en/Tutorial/Knob
  http://fritzing.org/projects/analog-input-to-servo/
  http://fritzing.org/projects/digital-input-button/
