# Fritzing sketch id3478_Muwoon_0 (saved by Fritzing 0.9.3b)
breadboards: 1

parts:
  Part1 = Arduino Uno (Rev3)
  SP1 = SPEAKER [package=pcb_mount_speaker]

nets:
  N1: Part1.A0, SP1.+
  N2: Part1.A2, SP1.-
