# Fritzing sketch id3479_ROBOT_SENSOR_2W_0 (saved by Fritzing 0.9.2b)
stripboards: 6

parts:
  R1 = Resistor [tolerance=±5% resistance=39k package=THT]
  Parte1 = Arduino Mega 2560 (Rev3)
  C1 = Ceramic Capacitor [capacitance=100nF voltage=35V package="100 mil [THT, multilayer]"]
  LED1 = LED - 3mm [color="Red (633nm)" package="3 mm [THT]"]
  LED2 = LED - 3mm [color="Green (560nm)" package="3 mm [THT]"]
  R5 = Resistor [tolerance=±5% resistance=680 package=THT]
  R2 = Resistor [tolerance=±5% resistance=10k package=THT]
  R6 = Resistor [tolerance=±5% resistance=1k package=THT]
  D1 = Rectifier Diode [part_number=1N4001 package="300 mil [THT]"]
  D2 = Rectifier Diode [part_number=1N4001 package="300 mil [THT]"]
  INTERRUPTOR_POSICION_1 = Toggle Switch [package=THT]
  VCC1 = Battery block 9V
  Power_plug_12_V = Power plug
  INTERRUPTOR_POSICION_2 = Toggle Switch [package=THT]
  LED3 = LED - 5mm [color="White (4500K)" package="5 mm [THT]"]
  LED5 = LED - 3mm [color="Yellow (595nm)" package="3 mm [THT]"]
  LED4 = LED - 3mm [color="Green (570nm)" package="3 mm [THT]"]
  LED10 = LED - 3mm [color="Red (633nm)" package="3 mm [THT]"]
  LED11 = LED - 3mm [color="Green (570nm)" package="3 mm [THT]"]
  LED12 = LED - 3mm [color="Yellow (595nm)" package="3 mm [THT]"]
  R7 = Resistor [tolerance=±5% resistance=680 package=THT]
  R8 = Resistor [tolerance=±5% resistance=680 package=THT]
  R9 = Resistor [tolerance=±5% resistance=680 package=THT]
  R10 = Resistor [tolerance=±5% resistance=680 package=THT]
  LED14 = LED - 5mm [color="White (4500K)" package="5 mm [THT]"]
  LED15 = LED - 3mm [color="Red (633nm)" package="3 mm [THT]"]
  LED16 = LED - 3mm [color="Yellow (595nm)" package="3 mm [THT]"]
  LED17 = LED - 3mm [color="Green (570nm)" package="3 mm [THT]"]
  R11 = Resistor [tolerance=±5% resistance=680 package=THT]
  R12 = Resistor [tolerance=±5% resistance=680 package=THT]
  R13 = Resistor [tolerance=±5% resistance=680 package=THT]
  R14 = Resistor [tolerance=±5% resistance=680 package=THT]
  R15 = Resistor [tolerance=±5% resistance=680 package=THT]
  R16 = Resistor [tolerance=±5% resistance=680 package=THT]
  R17 = Resistor [tolerance=±5% resistance=680 package=THT]
  LED13 = LED - 3mm [color="Red (633nm)" package="3 mm [THT]"]
  J1 = Basic Servo
  Parte2 = SRF05 Ultrasonic Rangefinder
  M1 = DC Motor
  M2 = DC Motor
  Parte3 = Bluetooth HC-05 Macho  # not connected
  S1 = Ponte-H L298N
  R20 = Resistor [tolerance=±5% resistance=220 package=THT]
  LED21 = LED - 5mm [color="Blue (430nm)" package="5 mm [THT]"]
  LED22 = LED - 5mm [color="Blue (430nm)" package="5 mm [THT]"]
  R21 = Resistor [tolerance=±5% resistance=220 package=THT]

nets:
  N1: R1.Pin_1, C1.1, R2.Pin_0
  GND: Parte1.GND, J1.gnd
  N2: Parte1.D11_PWM, J1.pulse
  5V: Parte1.5V, J1.vcc
  N3: Parte1.D2_PWM, Parte2.connector9
  N4: Parte1.D3_PWM, Parte2.connector10
  N5: Parte1.D4_PWM, S1.connector6
  N6: Parte1.D5_PWM, S1.connector5
  N7: Parte1.D6_PWM, S1.connector4
  N8: Parte1.D7_PWM, S1.connector3
  N9: C1.0, R2.Pin_1
  N10: LED1.cathode, R6.Pin_0
  N11: LED1.anode, D2.anode
  N12: LED2.cathode, R5.Pin_0
  N13: LED2.anode, D1.anode
  N14: R5.Pin_1, VCC1.-
  N15: R6.Pin_1, Power_plug_12_V.GND
  N16: INTERRUPTOR_POSICION_1.L1, VCC1.+
  N17: Power_plug_12_V.VCC, INTERRUPTOR_POSICION_2.COM
  N18: LED3.cathode, R9.Pin_1
  N19: LED5.cathode, R10.Pin_1
  N20: LED4.cathode, R7.Pin_1
  N21: LED10.cathode, R8.Pin_1
  N22: LED11.cathode, R15.Pin_1
  N23: LED12.cathode, R16.Pin_1
  N24: LED14.cathode, R13.Pin_1
  N25: LED15.cathode, R12.Pin_1
  N26: LED16.cathode, R14.Pin_1
  N27: LED17.cathode, R11.Pin_1
  N28: R17.Pin_1, LED13.cathode
  N29: M1.pin_1, S1.connector8
  N30: M1.pin_2, S1.connector7
  N31: M2.pin_1, S1.connector9
  N32: M2.pin_2, S1.connector10
  N33: R20.Pin_1, LED22.cathode, LED22.anode
  N34: LED21.cathode, R21.Pin_1

notes:
  EL DIVISOR DE TENSION VA CONECTADO EN PARALELO A LA ENTRADA DE ENERGIA DEL ARDUINO
  GND
  VIN ARDUINO
  EL INTERRUPTOR ES UNO SOLO PERO DE DOBLE VIA POR LO QUE SERIA SIMILAR A DOS QUE CAMBIAN DE POSICION EN EL MISMO MOMENTO
  ANALOG IN ARDUINO
  INT1  BAT ON
  INT1  EXT ON
  LEDS INDICADORES DE VOLTAJE
  LEDS INDICADORES DE DETECCION
  LEDS INDICADORES DESENSADO US DER
  LEDS INDICADORES DESENSADO US IZQ
  LEDS INDICADORES DE TIPO DE CONEXION
