# Fritzing sketch id347_BluetoothLedBrightness_0 (saved by Fritzing 0.9.2b)
breadboards: 1

parts:
  부품1 = Arduino Uno (Rev3)
  부품2 = HC-06
  LED1 = LED - 5mm [color="Red (633nm)" package="5 mm [THT]"]
  R1 = Resistor [tolerance=±5% resistance=220 package=THT]

nets:
  N1: 부품1.D9_PWM, LED1.anode
  N2: 부품1.D2, 부품2.connector13
  N3: 부품1.D3_PWM, 부품2.connector12
  N4: 부품1.5V, 부품2.connector15
  N5: 부품1.GND, 부품2.connector14, R1.Pin_0
  N6: LED1.cathode, R1.Pin_1
