# Fritzing sketch id3481_Rrobot_Lawnmower_2_0 (saved by Fritzing 0.7.7b)
breadboards: 1

parts:
  Arduino1 = Arduino
  M1 = DC Motor
  M2 = DC Motor
  S1 = Pushbutton [package="[THT]"]
  S2 = Pushbutton [package="[THT]"]
  LCD1 = LCD screen
  VCC1 = Battery block 9V
  Q1 = NPN-Transistor [package="TO92 [THT]"]
  Q2 = NPN-Transistor [package="TO92 [THT]"]
  Q3 = NPN-Transistor [package="TO92 [THT]"]
  Q4 = NPN-Transistor [package="TO92 [THT]"]
  Q5 = NPN-Transistor [package="TO92 [THT]"]
  Q6 = NPN-Transistor [package="TO92 [THT]"]
  Q7 = NPN-Transistor [package="TO92 [THT]"]
  Q8 = NPN-Transistor [package="TO92 [THT]"]
  R1 = Resistor [tolerance=±5% resistance=1k package=THT]
  R2 = Resistor [tolerance=±5% resistance=1k package=THT]
  R3 = Resistor [tolerance=±5% resistance=1k package=THT]
  R4 = Resistor [tolerance=±5% resistance=1k package=THT]
  R5 = Resistor [tolerance=±5% resistance=1k package=THT]
  R6 = Resistor [tolerance=±5% resistance=1k package=THT]
  R7 = Resistor [tolerance=±5% resistance=1k package=THT]
  R8 = Resistor [tolerance=±5% resistance=1k package=THT]
  R9 = Rotary Potentiometer (Small) [maximum_resistance=10kΩ]
  R10 = Resistor [tolerance=±5% resistance=1k package=THT]
  R11 = Resistor [tolerance=±5% resistance=1k package=THT]
  S3 = Pushbutton [package="[THT]"]
  S4 = Pushbutton [package="[THT]"]
  S5 = Pushbutton [package="[THT]"]
  S6 = Pushbutton [package="[THT]"]

nets (from the breadboard view):
  GND: Arduino1.GND, LCD1.VSS, LCD1.R/W, LCD1.LED-, VCC1.-, Q2.B, Q3.B, Q5.B, Q7.B, R9.leg2, R10.Pin_1, R11.Pin_1
  N1: Arduino1.D13, S1.Pin_3, S1.Pin_4, R11.Pin_0
  N2: Arduino1.D12, S2.Pin_3, S2.Pin_4, R10.Pin_0
  N3: Arduino1.D11, R7.Pin_0, R8.Pin_0
  N4: Arduino1.D10, R3.Pin_0, R4.Pin_0
  N5: Arduino1.D9, R1.Pin_0, R2.Pin_0
  N6: Arduino1.D8, LCD1.DB6
  N7: Arduino1.D7, LCD1.DB7
  N8: Arduino1.D6, R5.Pin_0, R6.Pin_0
  N9: Arduino1.D5, LCD1.DB5
  N10: Arduino1.D4, LCD1.DB4
  N11: Arduino1.D3, LCD1.E
  N12: Arduino1.D2, LCD1.RS
  +5V: Arduino1.+5V, S1.Pin_1, S1.Pin_2, S2.Pin_1, S2.Pin_2, LCD1.VDD, LCD1.LED+, R9.leg1
  N13: M1.pin_1, Q1.B, Q3.E
  N14: M1.pin_2, Q2.E, Q8.B
  N15: M2.pin_1, Q6.B, Q7.E
  N16: M2.pin_2, Q4.B, Q5.E
  N17: LCD1.V0, R9.wiper
  N18: VCC1.+, S3.Pin_1, S3.Pin_2
  N19: Q1.E, Q4.E, Q6.E, Q8.E, S5.Pin_3, S5.Pin_4
  N20: Q1.C, R3.Pin_1
  N21: Q2.C, R4.Pin_1
  N22: Q3.C, R2.Pin_1
  N23: Q4.C, R5.Pin_1
  N24: Q5.C, R8.Pin_1
  N25: Q6.C, R7.Pin_1
  N26: Q7.C, R6.Pin_1
  N27: Q8.C, R1.Pin_1
  N28: S3.Pin_3, S3.Pin_4, S4.Pin_1, S4.Pin_2
  N29: S4.Pin_3, S4.Pin_4, S6.Pin_1, S6.Pin_2
  N30: S5.Pin_1, S5.Pin_2, S6.Pin_3, S6.Pin_4
