# Fritzing sketch id3482_Untitled_Sketch_0 (saved by Fritzing 0.8.5b)
breadboards: 1

parts:
  Part1 = Arduino Uno (Rev3)
  U1 = QRE1113 [package=qre1113]
  U2 = QRE1113 [package=qre1113]
  U3 = QRE1113 [package=qre1113]
  R1 = Resistor [tolerance=±5% resistance=220 package=THT]
  R2 = Resistor [tolerance=±5% resistance=10k package=THT]
  R3 = Resistor [tolerance=±5% resistance=220 package=THT]
  R6 = Resistor [tolerance=±5% resistance=220 package=THT]
  R7 = Resistor [tolerance=±5% resistance=10k package=THT]
  R8 = Resistor [tolerance=±5% resistance=10k package=THT]
  IC1 = L293D [package=THT]
  IC2 = Hex Inverter Schmitt Trigger SN74HC14 [package="DIP (Dual Inline)"]  # not connected
  M1 = DC Motor
  M2 = DC Motor

nets:
  N1: Part1.A0, U2.C, R7.Pin_0
  N2: Part1.A1, U3.C, R8.Pin_1
  N3: Part1.A2, U1.A, R1.Pin_0
  N4: Part1.D9_PWM, IC1.In_4
  N5: Part1.D10_PWM/SS, IC1.In_2
  N6: Part1.D11_PWM/MOSI, IC1.Enable_2
  N7: Part1.D12/MISO, IC1.Enable_1
  N8: Part1.GND, U1.K, U1.E, U2.K, U2.E, U3.K, U3.E, IC1.0V
  N9: Part1.5V, R1.Pin_1, R2.Pin_1, R3.Pin_1, R6.Pin_0, R7.Pin_1, R8.Pin_0, IC1.+Vmotor, IC1.+V
  N10: U1.C, R2.Pin_0
  N11: U2.A, R3.Pin_0
  N12: U3.A, R6.Pin_1
  N13: IC1.Out_1_(_Controlled_by_Enable_1_), M1.pin_2
  N14: IC1.Out_2_(_Controlled_by_Enable_1_), M1.pin_1
  N15: IC1.Out_3_(_Controlled_by_Enable_2_), M2.pin_2
  N16: IC1.Out_4_(_Controlled_by_Enable_2_), M2.pin_1
