# Fritzing sketch id3483_robotForCat_0 (saved by Fritzing 0.9.3b)
breadboards: 1

parts:
  Composant1 = Arduino Uno (Rev3)
  IC1 = ULN2003A [package="SO16 [SMD]"]
  M1 = Stepper Motor - Unipolar

nets:
  N1: Composant1.D8, IC1.In_4
  N2: Composant1.D9_PWM, IC1.In_3
  N3: Composant1.D10_PWM/SS, IC1.In_2
  N4: Composant1.D11_PWM/MOSI, IC1.In_1
  N5: Composant1.GND, IC1.COM_-_Common
  N6: Composant1.5V, IC1.0V
  N7: IC1.Out_6, M1.D
  N8: IC1.Out_5, M1.COMMON_2
  N9: IC1.Out_4, M1.B
  N10: IC1.Out_3, M1.C
  N11: IC1.Out_2, M1.COMMON_1
  N12: IC1.Out_1, M1.A
