# Fritzing sketch id3484_Arm_0 (saved by Fritzing 0.9.2b)
circuit board: 31.0403cm x 17.9299cm
breadboards: 1

parts:
  M2 = Stepper Motor - Bipolar
  M4 = DC Motor
  IC3 = L293D [package=THT]
  M5 = DC Motor
  M1 = Stepper Motor - Bipolar
  Part1 = Arduino Mega 2560 (Rev3)
  IC4 = L293D [package=THT]
  IC1 = L293D [package=THT]
  M3 = Stepper Motor - Bipolar
  R1 = Rotary Potentiometer (Small) [maximum_resistance=100kΩ package=THT]
  R2 = Rotary Potentiometer (Small) [maximum_resistance=100kΩ package=THT]
  R3 = Rotary Potentiometer (Small) [maximum_resistance=100kΩ package=THT]
  R4 = Rotary Potentiometer (Small) [maximum_resistance=100kΩ package=THT]
  R5 = Rotary Potentiometer (Small) [maximum_resistance=100kΩ package=THT]
  Power_plug1 = Power plug
  IC2 = L293D [package=THT]

nets:
  N1: M2.A, IC3.Out_2_(_Controlled_by_Enable_1_)
  N2: M2.C, IC3.Out_1_(_Controlled_by_Enable_1_)
  N3: M2.B, IC3.Out_4_(_Controlled_by_Enable_2_)
  N4: M2.D, IC3.Out_3_(_Controlled_by_Enable_2_)
  N5: M4.pin_1, IC4.Out_2_(_Controlled_by_Enable_1_)
  N6: M4.pin_2, IC4.Out_1_(_Controlled_by_Enable_1_)
  N7: IC3.In_1, Part1.D40
  GND: IC3.0V, Part1.GND, IC4.0V, IC1.0V, Power_plug1.GND, IC2.0V
  N8: IC3.In_2, Part1.D38
  N9: IC3.+Vmotor, IC4.+Vmotor, IC1.+Vmotor, Power_plug1.VCC, IC2.+Vmotor
  N10: IC3.In_3, Part1.D36
  N11: IC3.In_4, Part1.D34
  N12: IC3.+V, Part1.5V, IC4.+V, IC1.+V, IC2.+V
  N13: M5.pin_1, IC4.Out_3_(_Controlled_by_Enable_2_)
  N14: M5.pin_2, IC4.Out_4_(_Controlled_by_Enable_2_)
  N15: M1.A, IC2.Out_2_(_Controlled_by_Enable_1_)
  N16: M1.C, IC2.Out_1_(_Controlled_by_Enable_1_)
  N17: M1.B, IC2.Out_4_(_Controlled_by_Enable_2_)
  N18: M1.D, IC2.Out_3_(_Controlled_by_Enable_2_)
  N19: Part1.A0, R3.wiper
  N20: Part1.A1, R2.wiper
  N21: Part1.A2, R5.wiper
  N22: Part1.A3, R4.wiper
  N23: Part1.A4, R1.wiper
  N24: Part1.D2_PWM, IC4.In_4
  N25: Part1.D3_PWM, IC4.In_3
  N26: Part1.D5_PWM, IC4.In_2
  N27: Part1.D6_PWM, IC4.In_1
  N28: Part1.D24, IC1.In_4
  N29: Part1.D26, IC1.In_3
  N30: Part1.D28, IC1.In_2
  N31: Part1.D30, IC1.In_1
  N32: Part1.D44, IC2.In_4
  N33: Part1.D46, IC2.In_3
  N34: Part1.D48, IC2.In_2
  N35: Part1.D50, IC2.In_1
  N36: IC1.Out_1_(_Controlled_by_Enable_1_), M3.D
  N37: IC1.Out_2_(_Controlled_by_Enable_1_), M3.B
  N38: IC1.Out_3_(_Controlled_by_Enable_2_), M3.C
  N39: IC1.Out_4_(_Controlled_by_Enable_2_), M3.A
  N40: R1.leg2, R2.leg2, R3.leg2, R4.leg2, R5.leg2

notes:
  Motor 1 (Base)
  Motor 2
  Motor 3
  Motor 4
  (End Effector)
  Motor 5
  For
  Motor 3
  For
  Motor 4
  For Motor 5
  For Motor 2
  For Motor 1
  Power In (12v)
