# Fritzing sketch id3486_Reciever_Circuit_0 (saved by Fritzing 0.9.2b)
breadboards: 1

parts:
  Part1 = Arduino Uno (Rev3)
  S1 = Toggle Switch [package=THT]
  M1 = DC Motor
  U1 = L298_BRIDGE_DRIVER [package=powerso20]
  M2 = DC Motor
  U2 = mystery part, 4 pins [chip_label=?]
  VCC1 = Battery
  VCC2 = Battery

nets:
  N1: Part1.D9_PWM, U1.IN4
  N2: Part1.D2, U2.pin2
  N3: Part1.D3_PWM, U1.IN1
  N4: Part1.D5_PWM, U1.IN2
  N5: Part1.D6_PWM, U1.IN3
  N6: Part1.5V, U1.VS, U1.ENA, U1.ENB, U2.pin4
  N7: Part1.GND, S1.L1
  N8: S1.COM, U1.GND, U2.pin1, VCC2.+
  N9: M1.pin_1, U1.OUT2
  N10: M1.pin_2, U1.OUT1
  N11: U1.VSS, VCC1.-
  N12: U1.OUT3, M2.pin_2
  N13: U1.OUT4, M2.pin_1
  N14: VCC1.+, VCC2.-

notes:
  RF 433MHz Rx
