# Fritzing sketch id3487_Transmitter_Circuit_0 (saved by Fritzing 0.9.2b)
breadboards: 2

parts:
  S1 = Pushbutton [package="[THT]"]
  S2 = Pushbutton [package="[THT]"]
  S3 = Pushbutton [package="[THT]"]
  S4 = Pushbutton [package="[THT]"]
  S5 = Pushbutton [package="[THT]"]
  U1 = mystery part, 3 pins [chip_label=?]
  Part1 = Arduino Nano (Rev3.0)
  R1 = Resistor [tolerance=±5% resistance=10k package=THT]
  R2 = Resistor [tolerance=±5% resistance=10k package=THT]
  R3 = Resistor [tolerance=±5% resistance=10k package=THT]
  R4 = Resistor [tolerance=±5% resistance=10k package=THT]
  R5 = Resistor [tolerance=±5% resistance=10k package=THT]

nets:
  N1: S1.Pin_1, S1.Pin_2, Part1.D12/MISO, R1.Pin_0
  N2: S1.Pin_3, S1.Pin_4, S2.Pin_3, S2.Pin_4, S3.Pin_3, S3.Pin_4, S4.Pin_3, S4.Pin_4, S5.Pin_3, S5.Pin_4, U1.pin3, Part1.GND
  N3: S2.Pin_1, S2.Pin_2, Part1.D11/MOSI, R2.Pin_0
  N4: S3.Pin_1, S3.Pin_2, Part1.D10, R3.Pin_0
  N5: S4.Pin_1, S4.Pin_2, Part1.D9, R4.Pin_0
  N6: S5.Pin_1, S5.Pin_2, Part1.D8, R5.Pin_0
  N7: U1.pin1, Part1.D3
  N8: U1.pin2, Part1.5V, R1.Pin_1, R2.Pin_1, R3.Pin_1, R4.Pin_1, R5.Pin_1

notes:
  RF 433MHz Tx
