# Fritzing sketch id3489_robotic_wrist_with_speaker_graceyoo_0 (saved by Fritzing 0.8.5b)
breadboards: 1

parts:
  J1 = Basic Servo
  J2 = Basic Servo
  IR1 = TSOP312.., 314.. [package=THT]
  Part1 = Arduino Uno (Rev3)
  J3 = Piezo Speaker

nets:
  GND: J1.gnd, J2.gnd, IR1.GND, Part1.GND, J3.pin1
  VCC: J1.vcc, J2.vcc, IR1.Vs, Part1.5V
  N1: J1.pulse, Part1.D9_PWM
  N2: J2.pulse, Part1.D10_PWM/SS
  N3: IR1.Data, Part1.D11_PWM/MOSI
  N4: Part1.D12/MISO, J3.pin2
