# Fritzing sketch id3490_Bluetooth.txt_0 (saved by Fritzing 0.9.3b)

parts:
  Part2 = Arduino Uno (Rev3)
  M1 = DC Motor
  M2 = DC Motor
  J1 = Piezo Speaker
  Part3 = Max Power IR LED Kit
  Part4 = Bluetooth HC-05 Macho
  VCC1 = Battery block 9V
  VCC2 = Battery block 9V

nets:
  N1: Part2.D9_PWM, M2.pin_2
  N2: Part2.D11_PWM/MOSI, M1.pin_1
  N3: Part2.D13/SCK, M1.pin_2
  GND: Part2.GND, J1.pin1, Part3.GND, Part4.GND, VCC1.-, VCC2.-
  N4: Part2.D0/RX, Part4.TXD
  N5: Part2.D1/TX, Part4.RXD
  N6: Part2.D4, Part3.CONTROL
  N7: Part2.D5_PWM, J1.pin2
  N8: Part2.D7, M2.pin_1
  3V3: Part2.3V3, Part4.VCC
  5V: Part2.5V, Part3.VCC
  N9: Part2.VIN, VCC1.+, VCC2.+
