# Fritzing sketch id3491_rock_paper_scissors_diagram_0 (saved by Fritzing 0.8.7b)
breadboards: 1

parts:
  Part1 = Arduino Uno (Rev3)
  U1 = SLIDER [package=slider]  # not connected
  LED1 = LED - 5mm [color="Yellow (595nm)" package="5 mm [THT]"]
  LED2 = LED - 5mm [color="Yellow (595nm)" package="5 mm [THT]"]
  LED3 = LED - 5mm [color="Yellow (595nm)" package="5 mm [THT]"]
  R1 = Resistor [tolerance=±5% resistance=220 package=THT]
  R2 = Resistor [tolerance=±5% resistance=220 package=THT]
  R3 = Resistor [tolerance=±5% resistance=220 package=THT]
  J1 = Piezo Speaker
  LED4 = LED - 5mm [color="Red (633nm)" package="5 mm [THT]"]
  LED5 = LED - 5mm [color="Red (633nm)" package="5 mm [THT]"]
  LED6 = LED - 5mm [color="Red (633nm)" package="5 mm [THT]"]
  R4 = Resistor [tolerance=±5% resistance=220 package=THT]
  R5 = Resistor [tolerance=±5% resistance=220 package=THT]
  R6 = Resistor [tolerance=±5% resistance=220 package=THT]

nets:
  N1: Part1.D8, J1.pin2
  N2: Part1.D9_PWM, R1.Pin_1
  N3: Part1.D10_PWM/SS, R2.Pin_1
  N4: Part1.D11_PWM/MOSI, R3.Pin_1
  N5: Part1.GND, LED1.cathode, LED2.cathode, LED3.cathode, J1.pin1, R4.Pin_1, R5.Pin_1, R6.Pin_1
  N6: Part1.D2, LED4.anode
  N7: Part1.D3_PWM, LED5.anode
  N8: Part1.D4, LED6.anode
  N9: LED1.anode, R3.Pin_0
  N10: LED2.anode, R2.Pin_0
  N11: LED3.anode, R1.Pin_0
  N12: LED4.cathode, R4.Pin_0
  N13: LED5.cathode, R5.Pin_0
  N14: LED6.cathode, R6.Pin_0
