# Fritzing sketch id3492_Untitled_Sketch_0 (saved by Fritzing 0.9.3b)
breadboards: 1

parts:
  R1 = Resistor [tolerance=±5% resistance=220 package="0603 [SMD]"]
  R2 = Resistor [tolerance=±5% resistance=220 package="0603 [SMD]"]
  U1 = MPL3115A2 [package=lga8]
  Part3 = Triple Axis Accelerometer Breakout - ADXL335
  Part4 = Arduino Mega 2560 (Rev3)
  Part5 = BME280 Breakout
  U2 = TMP102 [package=sot563]
  GY-NEO6MV3 = SUP500F [package=sup500f]
  R4 = Resistor [tolerance=±5% resistance=10k package="1206 [SMD]"]
  R5 = Resistor [tolerance=±5% resistance=4.7k package="1206 [SMD]"]

nets:
  N1: R1.Pin_0, Part4.D2_PWM
  N2: R1.Pin_1, R2.Pin_1
  N3: R2.Pin_0, Part4.D3_PWM
  VCC: U1.VDD, Part3.VCC, Part4.5V, U2.VCC, GY-NEO6MV3.TX-O
  GND: U1.GND, Part3.GND, Part4.GND, Part5.GND, U2.GND, U2.ADD0
  N4: Part3.ZOUT, Part4.D53
  N5: Part3.YOUT, Part4.D52
  N6: Part3.XOUT, Part4.D51
  3V3: Part4.3V3, Part5.3.3V
  N7: Part4.D34, GY-NEO6MV3.VCC
  N8: Part4.D35, R5.Pin_0
  N9: Part4.D36, U2.SDA
  N10: Part4.D37, U2.SCL
  N11: Part4.D43, Part5.SCK/SCL
  N12: Part4.D44, Part5.!CS
  N13: Part4.D45, Part5.SDO/ADR
  N14: Part4.D46, Part5.SDI/SDA
  N15: GY-NEO6MV3.RX-I, R4.Pin_0
  N16: GY-NEO6MV3.GND, R4.Pin_1, R5.Pin_1
