# Fritzing sketch id3493_Rocket_LED_Countdown_0 (saved by Fritzing 0.7.0b)
breadboards: 1

parts:
  Arduino1 = Arduino
  LED1 = LED - 5mm [color="Red (633nm)" package="5 mm [THT]"]
  LED2 = LED - 5mm [color="Red (633nm)" package="5 mm [THT]"]
  LED3 = LED - 5mm [color="Red (633nm)" package="5 mm [THT]"]
  LED4 = LED - 5mm [color="Red (633nm)" package="5 mm [THT]"]
  LED5 = LED - 5mm [color="Red (633nm)" package="5 mm [THT]"]
  K1 = Relay [part_number=FRS1B-S package=THT]
  VCC1 = Battery
  S1 = Pushbutton [package=THT]
  R1 = Resistor [tolerance=±5% resistance=220 package=THT]
  R2 = Resistor [tolerance=±5% resistance=220 package=THT]

nets (from the pcb view):
  N1: Arduino1.GND, LED1.cathode, LED2.cathode, LED3.cathode, LED4.cathode, LED5.cathode, K1.COIL1, R1.Pin_1, R2.Pin_0, R2.Pin_1
  N2: Arduino1.D7, S1.leg0, R1.Pin_0
  N3: Arduino1.D6, K1.COIL2
  N4: Arduino1.D5, LED5.anode
  N5: Arduino1.D4, LED2.anode
  N6: Arduino1.D3, LED3.anode
  N7: Arduino1.D2, LED1.anode
  N8: Arduino1.D1TX, LED4.anode
  N9: Arduino1.+5V, S1.leg1
  N10: K1.B, VCC1.-

notes:
  Rocket Countdown 3000
  To Kill:
  Cut the Gray Wire
  Hold Button to Start
