# Fritzing sketch id3496_rompeeker_0 (saved by Fritzing 0.8.5b)
circuit board: 8.46667cm x 5.64444cm
breadboards: 2

parts:
  Part1 = Arduino Mega 2560 (Rev3)
  LCD1 = LCD screen
  S1 = Pushbutton [package="[THT]"]
  R1 = Trimmer Potentiometer [maximum_resistance=10kΩ package=THT]
  R2 = Trimmer Potentiometer [maximum_resistance=10kΩ package=THT]
  IC1 = IC, DIP package, 28 pins [chip_label=ROM]
  R3 = Resistor [tolerance=±5% resistance=1k package=THT]
  VCC1 = Battery block 9V

nets:
  N1: Part1.A0, LCD1.RS
  N2: Part1.A1, LCD1.E
  N3: Part1.A2, LCD1.DB4
  N4: Part1.A3, LCD1.DB5
  N5: Part1.A4, LCD1.DB6
  N6: Part1.A5, LCD1.DB7
  N7: Part1.A7, S1.Pin_1, S1.Pin_2, R3.Pin_1
  GND: Part1.GND, LCD1.VSS, LCD1.R/W, LCD1.LED-, R1.leg2, R2.leg2, IC1.pin1, IC1.pin14, IC1.pin20, IC1.pin22, R3.Pin_0, VCC1.-
  5V: Part1.5V, LCD1.VDD, S1.Pin_3, S1.Pin_4, R1.leg1, R2.leg1, IC1.pin28
  N8: Part1.VIN, VCC1.+
  N9: Part1.D22, IC1.pin10
  N10: Part1.D23, IC1.pin9
  N11: Part1.D24, IC1.pin8
  N12: Part1.D25, IC1.pin7
  N13: Part1.D26, IC1.pin6
  N14: Part1.D27, IC1.pin5
  N15: Part1.D28, IC1.pin4
  N16: Part1.D29, IC1.pin3
  N17: Part1.D30, IC1.pin25
  N18: Part1.D31, IC1.pin24
  N19: Part1.D32, IC1.pin21
  N20: Part1.D33, IC1.pin23
  N21: Part1.D34, IC1.pin2
  N22: Part1.D35, IC1.pin26
  N23: Part1.D36, IC1.pin27
  N24: Part1.D46, IC1.pin11
  N25: Part1.D47, IC1.pin12
  N26: Part1.D48, IC1.pin13
  N27: Part1.D49, IC1.pin15
  N28: Part1.D50, IC1.pin16
  N29: Part1.D51, IC1.pin17
  N30: Part1.D52, IC1.pin18
  N31: Part1.D53, IC1.pin19
  N32: LCD1.V0, R1.wiper
  N33: LCD1.LED+, R2.wiper

notes:
  ROM Peeker, Byte for byte peek into the 28 pin SEGA Master System ROM chip extracted from a cartridge, 1.0
