# Fritzing sketch id3497_Room_Security_System_0 (saved by Fritzing 0.9.3b)
circuit board: 6.82102cm x 5.36232cm
breadboards: 1

parts:
  Part1 = Arduino Uno (Rev3)
  R_>_G_led = Resistor [tolerance=±5% resistance=220 package="2512 [SMD]"]
  R_>_G_btn = Resistor [tolerance=±5% resistance=220 package="2512 [SMD]"]
  R_>_S = Resistor [tolerance=±5% resistance=220 package="2512 [SMD]"]
  R_>_B_btn = Resistor [tolerance=±5% resistance=220 package="2512 [SMD]"]
  R_>_R_btn = Resistor [tolerance=±5% resistance=220 package="2512 [SMD]"]
  R_>_R_led = Resistor [tolerance=±5% resistance=220 package="2512 [SMD]"]
  Blue_Btn = Pushbutton [package="[THT]"]
  Red_Btn = Pushbutton [package="[THT]"]
  Yellow_Btn = Pushbutton [package="[THT]"]
  Buzzer = Piezo Speaker
  Red_led = LED - 5mm [color="Red (633nm)" package="5 mm [THT]"]
  Sensor = mag-door [part_number=Sensor]
  Green_Btn = Pushbutton [package="[THT]"]
  Green_led = smd LED [color="Green (555nm)" package="1206 [SMD]"]  # not connected
  R_>_Y_btn = Resistor [tolerance=±5% resistance=220 package="2512 [SMD]"]

nets (from the schematic view):
  N1: Part1.A0, Red_led.anode
  N2: Part1.GND, R_>_G_led.Pin_0, R_>_S.Pin_0, R_>_R_led.Pin_0, Buzzer.pin1
  N3: Part1.D2, R_>_B_btn.Pin_1, Blue_Btn.Pin_3, Blue_Btn.Pin_4
  N4: Part1.D3_PWM, R_>_R_btn.Pin_1, Red_Btn.Pin_3, Red_Btn.Pin_4
  N5: Part1.D4, Yellow_Btn.Pin_3, Yellow_Btn.Pin_4, R_>_Y_btn.Pin_1
  N6: Part1.D5_PWM, R_>_G_btn.Pin_1, Green_Btn.Pin_3, Green_Btn.Pin_4
  N7: Part1.D6_PWM, R_>_S.Pin_1, Sensor.connector1
  N8: Part1.D7, Buzzer.pin2
  N9: Part1.3V3, Blue_Btn.Pin_1, Blue_Btn.Pin_2, Red_Btn.Pin_1, Red_Btn.Pin_2, Yellow_Btn.Pin_1, Yellow_Btn.Pin_2, Sensor.connector0, Green_Btn.Pin_1, Green_Btn.Pin_2
  N10: R_>_G_btn.Pin_0, R_>_B_btn.Pin_0, R_>_R_btn.Pin_0, R_>_Y_btn.Pin_0
  N11: R_>_R_led.Pin_1, Red_led.cathode
