# Fritzing sketch id3498_Arduino__Fritzing_File_0 (saved by Fritzing 0.9.3b)
circuit board: 5.12936cm x 4.90624cm
breadboards: 1

parts:
  10_nF_Capacitor = Ceramic Capacitor [capacitance=10nF package="100 mil [THT, multilayer]"]
  10_nF_Capacitor_2 = Ceramic Capacitor [capacitance=10nF package="100 mil [THT, multilayer]"]
  10kΩ_Resistor = Resistor [tolerance=±5% resistance=10k package=THT]
  10kΩ_Resistor_2 = Resistor [tolerance=±5% resistance=10k package=THT]
  10kΩ_Resistor_3 = Resistor [tolerance=±5% resistance=10k package=THT]
  10kΩ_Resistor_4 = Resistor [tolerance=±5% resistance=10k package=THT]
  50V_1000µF_Capacitor = Electrolytic Capacitor [capacitance=1mF voltage=50V package="100 mil [THT, electrolytic]"]
  Rotary_Encoder = prefix0000
  Arduino_Micro = Arduino Micro (Rev3)
  NEOPIXEL1 = adafruit [part_number=1461]

nets:
  N1: 10_nF_Capacitor.0, 10_nF_Capacitor_2.1, 50V_1000µF_Capacitor.-, Rotary_Encoder.connector2, Rotary_Encoder.connector4, Arduino_Micro.GND, NEOPIXEL1.connector3, NEOPIXEL1.connector4
  N2: 10_nF_Capacitor.1, 10kΩ_Resistor_3.Pin_0, Arduino_Micro.D2/SDA
  N3: 10_nF_Capacitor_2.0, 10kΩ_Resistor_2.Pin_1, Arduino_Micro.D3/SCL
  N4: 10kΩ_Resistor.Pin_0, 10kΩ_Resistor_2.Pin_0, Rotary_Encoder.connector3
  N5: 10kΩ_Resistor.Pin_1, 10kΩ_Resistor_4.Pin_1, 50V_1000µF_Capacitor.+, Arduino_Micro.5V, NEOPIXEL1.connector1, NEOPIXEL1.connector6
  N6: 10kΩ_Resistor_3.Pin_1, 10kΩ_Resistor_4.Pin_0, Rotary_Encoder.connector1
  N7: Rotary_Encoder.connector5, Arduino_Micro.D4_PWM/A6
  N8: Arduino_Micro.D6_PWM/A7, NEOPIXEL1.connector2
