# Fritzing sketch id349_BluetoothRcCar_0 (saved by Fritzing 0.9.2b)
breadboards: 1

parts:
  부품1 = Arduino Uno (Rev3)
  부품2 = HC-06

nets:
  N1: 부품1.D8, 부품2.connector13
  N2: 부품1.D9_PWM, 부품2.connector12
  N3: 부품1.5V, 부품2.connector15
  N4: 부품1.GND, 부품2.connector14

notes:
  6V GND
  6V VCC
  L9110S
  GND
  L9110S
  VCC
  L9110S
  B-IB
  L9110S
  B-IA
  L9110S
  A-IB
  L9110S
  A-IA
