# Fritzing sketch id34_Untitled_Sketch2222_0 (saved by Fritzing 0.8.7b)
circuit board: 4.13169cm x 2.54487cm
breadboards: 1

parts:
  U1 = LM 358 Dual Op-Amp [package="DIP8 [THT]"]
  R1 = Resistor [tolerance=±5% resistance=10k package=THT]
  R2 = Resistor [tolerance=±5% resistance=1k package=THT]
  R5 = Resistor [tolerance=±5% resistance=100 package=THT]
  C1 = Electrolytic Capacitor [capacitance=0.1mF voltage=20V package="100 mil [THT, electrolytic]"]
  R7 = Resistor [tolerance=±5% resistance=100k package=THT]
  R8 = Resistor [tolerance=±5% resistance=100k package=THT]
  R9 = Resistor [tolerance=±5% resistance=100k package=THT]
  C5 = Electrolytic Capacitor [capacitance=10µF voltage=20V package="100 mil [THT, electrolytic]"]
  R10 = Resistor [tolerance=±5% resistance=1k package=THT]
  C6 = Ceramic Capacitor [capacitance=1µF package="100 mil [THT, multilayer]"]
  J1 = Screw terminal - 2 pins [package=THT]
  J2 = Screw terminal - 2 pins [package=THT]
  J3 = Screw terminal - 2 pins [package=THT]
  C4 = Electrolytic Capacitor [capacitance=0.1mF voltage=20V package="100 mil [THT, electrolytic]"]

nets:
  N1: U1.connector0, R1.Pin_1, R5.Pin_0
  N2: U1.connector1, R1.Pin_0, R2.Pin_1
  N3: U1.connector2, R8.Pin_1, R9.Pin_0, C5.+
  GND: U1.connector3, R7.Pin_1, R9.Pin_1, C6.0, J1.pin2, J2.pin2, J3.pin2, C4.-
  12V: U1.connector7, R8.Pin_0, J3.pin1
  N4: R2.Pin_0, C4.+
  N5: R5.Pin_1, C1.+
  N6: C1.-, R7.Pin_0, J1.pin1
  N7: C5.-, R10.Pin_1, C6.1
  N8: R10.Pin_0, J2.pin1
