# Fritzing sketch id3501_SKRM_breakout10_0 (saved by Fritzing 0.9.1b)
circuit board: 5.63244cm x 2.96305cm
breadboards: 1

parts:
  C1 = Ceramic Capacitor [capacitance=100nF package="100 mil [THT, multilayer]"]
  J3 = female pin header, 8 pins [form="♀ (female)"]
  J4 = female pin header, 5 pins [form="♀ (female)"]
  J5 = female pin header, 5 pins [form="♀ (female)"]
  J1 = double row female pin header, 16 pins [form="♀ (female)"]
  IC1 = IC, DIP package, 16 pins [chip_label=74HC148]
  RPACK = mystery part, 9 pins [chip_label="10k Resistor pack"]

nets:
  +3.3V: C1.0, J5.pin1, J1.pin11, IC1.pin16, RPACK.pin9
  GND: C1.1, J4.pin1, J1.pin1, J1.pin7, J1.pin10, IC1.pin5, IC1.pin8
  N1: J3.pin1, IC1.pin4, RPACK.pin1
  N2: J3.pin2, IC1.pin3, RPACK.pin2
  N3: J3.pin3, IC1.pin2, RPACK.pin3
  N4: J3.pin4, IC1.pin1, RPACK.pin4
  SW5: J3.pin5, IC1.pin13, RPACK.pin5
  SW6: J3.pin6, IC1.pin12, RPACK.pin6
  SW7: J3.pin7, IC1.pin11, RPACK.pin7
  SW8: J3.pin8, IC1.pin10, RPACK.pin8
  FROM_MOD_L: J4.pin2, J1.pin2
  P_1: J4.pin3, J1.pin3
  CLIP: J4.pin4, J1.pin6
  TO_MOD: J4.pin5, J1.pin8, J1.pin9
  P_0: J5.pin2, J1.pin13
  P_2: J5.pin3, J1.pin14
  FROM_MOD_R: J5.pin4, J1.pin15
  +12V: J5.pin5, J1.pin16
  S_2: J1.pin4, IC1.pin6
  S_0: J1.pin5, IC1.pin9
  S_1: J1.pin12, IC1.pin7

notes:
  SKRM-connector
  Rotary-connector
  SKRM 1.0 2015
  12V
  GND
  R
  L
  P_1
  CLP
  IN
  P_2
  P_0
  3V3
  1
  16
  2
  3
  4
  5
  6
  7
  8
  R. SWITCH
  IC1
  DIYcrap
