# Fritzing sketch id3502_Motore_0 (saved by Fritzing 0.7.7b)
breadboards: 1

parts:
  Arduino1 = Arduino
  IC1 = H-Bridge [package=THT]
  S2 = Pushbutton [package="[THT]"]  # not connected
  S1 = Pushbutton [package="[THT]"]  # not connected
  S3 = Pushbutton [package="[THT]"]
  S4 = Pushbutton [package="[THT]"]
  M1 = Stepper Motor - Bipolar

nets:
  GND: Arduino1.GND, IC1.GND1, IC1.GND2, IC1.GND3, IC1.GND4, S3.Pin_1, S3.Pin_2, S4.Pin_1, S4.Pin_2
  N1: Arduino1.D11, IC1.4A
  N2: Arduino1.D10, IC1.3A
  N3: Arduino1.D9, IC1.1A
  N4: Arduino1.D8, IC1.2A
  N5: Arduino1.D5, S3.Pin_3, S3.Pin_4
  N6: Arduino1.D4, S4.Pin_3, S4.Pin_4
  N7: Arduino1.+5V, IC1.1_2EN, IC1.3_4EN, IC1.VCC1
  N8: IC1.1Y, M1.A
  N9: IC1.2Y, M1.C
  N10: IC1.3Y, M1.B
  N11: IC1.4Y, M1.D

notes:
  Switch di fine corsa
  2,3 - Rotazione
  4,5 - Fine corsa
  8,9,10,11 - Motore
  12V
  Motore passo-passo
