# Fritzing sketch id3506_IN_12d_Socket_1_0 (saved by Fritzing 0.8.7b)
circuit board: 5cm x 6cm
breadboards: 1

parts:
  J3 = male pin header, 18 pins [form="♂ (male)" part_number=IN-12As]
  U1 = M74HC238 [package=dil16]
  SW1 = DIP Switch 8 Position [package=dipswitch-08]
  Q1 = NPN-Transistor [part_number=MPSA42 package="TO92 [THT]"]
  R4 = Resistor [tolerance=±5% resistance=390k package=THT]
  Q2 = NPN-Transistor [part_number=MPSA92 package="TO92 [THT]"]
  R5 = Resistor [tolerance=±5% resistance=8.2k package=THT]
  J5 = male pin header, 12 pins [form="♂ (male)" part_number="IN-12A Socket"]
  J4 = male pin header, 18 pins [form="♂ (male)" part_number=IN-12As]

nets:
  N1: J3.pin1, J5.pin1, J4.pin1
  N2: J3.pin2, J5.pin2, J4.pin2
  N3: J3.pin3, J5.pin3, J4.pin3
  N4: J3.pin4, J5.pin4, J4.pin4
  N5: J3.pin5, J5.pin5, J4.pin5
  N6: J3.pin6, J5.pin6, J4.pin6
  N7: J3.pin7, J5.pin7, J4.pin7
  N8: J3.pin8, J5.pin8, J4.pin8
  N9: J3.pin9, J5.pin9, J4.pin9
  N10: J3.pin10, J5.pin10, J4.pin10
  N11: J3.pin11, J5.pin11, J4.pin11
  N12: J3.pin12, U1.A, J4.pin12
  N13: J3.pin13, U1.B, J4.pin13
  N14: J3.pin14, U1.C, J4.pin14
  5V: J3.pin15, U1.VCC, J4.pin15
  GND: J3.pin16, J3.pin17, U1.GND, Q1.E, J4.pin16, J4.pin17
  180V: J3.pin18, R5.Pin_1, J4.pin18
  N15: U1.Y7, SW1.16
  N16: U1.Y6, SW1.15
  N17: U1.Y5, SW1.14
  N18: U1.Y4, SW1.13
  N19: U1.Y3, SW1.12
  N20: U1.Y2, SW1.11
  N21: U1.Y1, SW1.10
  N22: U1.Y0, SW1.9
  N23: SW1.1, SW1.2, SW1.3, SW1.4, SW1.5, SW1.6, SW1.7, SW1.8, Q1.B
  N24: Q1.C, R4.Pin_0
  N25: R4.Pin_1, Q2.B
  N26: Q2.E, J5.pin12
  N27: Q2.C, R5.Pin_0
