# Fritzing sketch id3509_ROV_Sensors_0 (saved by Fritzing 0.9.3b)
breadboards: 1

parts:
  Part1 = Arduino Mega 2560 (Rev3)
  U1 = Hirose DF13 Series Header [part_number=DF13#-4P-1.25V package=DF13C-4P-1.25V]
  Part2 = Triple Axis Accelerometer Breakout - ADXL345
  Part3 = Bluetooth HC-05 Macho
  DHT1 = DHT11_Temperature_and_Humitidy_Sensor
  R1 = Resistor [tolerance=±5% resistance=10k package=THT]

nets:
  N1: Part1.D21/SCL, Part1.SCL, U1.3, Part2.SCL
  N2: Part1.D20/SDA, Part1.SDA, U1.2, Part2.SDA
  N3: Part1.D10_PWM, Part3.RXD
  N4: Part1.D8_PWM, Part3.TXD
  N5: Part1.D2_PWM, DHT1.connector2, R1.Pin_0
  VCC: Part1.5V, U1.1, Part2.VCC, Part3.VCC, DHT1.connector1, R1.Pin_1
  GND: Part1.GND, U1.4, Part2.GND, Part3.GND, DHT1.connector4

notes:
  5v side
  Sea Sweepers ROV
