# Fritzing sketch id350_BluetoothRgbLed_0 (saved by Fritzing 0.9.2b)
breadboards: 1

parts:
  부품1 = Arduino Uno (Rev3)
  부품2 = HC-06
  LED2 = RGB LED (com. cathode, rgb) [package="5 mm [THT]"]

nets:
  N1: 부품1.D9_PWM, LED2.red_anode
  N2: 부품1.D10_PWM/SS, LED2.green_anode
  N3: 부품1.D11_PWM/MOSI, LED2.blue_anode
  N4: 부품1.D2, 부품2.connector13
  N5: 부품1.D3_PWM, 부품2.connector12
  N6: 부품1.5V, 부품2.connector15
  N7: 부품1.GND, 부품2.connector14, LED2.common_cathode
