# Fritzing sketch id3511_slaveSetup_0 (saved by Fritzing 0.9.3b)

parts:
  Part2 = XBee Explorer Regulated
  Part3 = LSM303C (6 DOF)
  U1 = LIPO-2000mAh [package=lipo-2000]
  J1 = Power Jack [package=power_jack_pth_lock]
  Part4 = Arduino Uno (Rev3)

nets (from the schematic view):
  N1: Part2.DIN, Part4.D2
  N2: Part2.DOUT, Part4.D3_PWM
  5V: Part2.5V, Part4.5V
  GND: Part2.GND, Part4.GND
  N3: Part3.SDA/SDI/SDO, Part4.A4/SDA
  N4: Part3.SCL/SCLK, Part4.A5/SCL
  VCC: Part3.VCC, Part4.3V3
  N5: U1.+, J1.GND
  N6: U1.-, J1.GNDBREAK, Part4.VIN
