# Fritzing sketch id3512_Raspberry_Pi_transistor_circuit_only_0 (saved by Fritzing 0.9.3b)
breadboards: 1

parts:
  LS1 = Piezo Speaker [part_number=AB3452]
  Raspberry_Pi_3 = Raspberry Pi 3 [part_number=RPI-3-V1.2]
  K1 = RELAY-SOLIDSTATE [part_number="SSR-40 DA" package=relay-s108t02]
  R1 = Resistor [tolerance=±1% resistance=1k package="1206 [SMD]"]
  R2 = Resistor [tolerance=±2% resistance=1k package="1206 [SMD]"]
  Q1 = TRANSISTOR_NPN [part_number=2N3904 package=to-92-ammo]
  Q2 = TRANSISTOR_NPN [part_number=2N3904 package=to-92-ammo]

nets:
  12V: LS1.pin1, K1.+
  N1: LS1.pin2, Q2.C
  GND: Raspberry_Pi_3.GND, Q1.E, Q2.E
  N2: Raspberry_Pi_3.GPIO21, R1.Pin_0
  N3: Raspberry_Pi_3.GPIO23, R2.Pin_0
  N4: K1.-, Q1.C
  N5: R1.Pin_1, Q1.B
  N6: R2.Pin_1, Q2.B
