# Fritzing sketch id3513_RPi_ARD_program_reset_circuit_0 (saved by Fritzing 0.9.3b)
circuit board: 8.46667cm x 5.64444cm

parts:
  SW1 = SWITCH-DPDT [package=gpi-152-3013]
  JP1 = Header 4 [package=screwterminal-3.5mm-4_lock]
  JP2 = Header 4 [package=screwterminal-3.5mm-4_lock]
  U1-RST = RELAY [package=relay-t9a-2]
  R1 = Resistor [tolerance=±5% resistance=10k package="0603 [SMD]"]
  R2 = Resistor [tolerance=±5% resistance=10k package="0603 [SMD]"]

nets:
  N1: SW1.2, JP1.1
  N2: SW1.5, JP2.1
  NC: SW1.1
  N3: SW1.4, R1.Pin_1
  N4: SW1.3, U1-RST.NO
  N5: SW1.6, R2.Pin_1
  N6: JP1.2, U1-RST.MAIN
  N7: JP1.3, U1-RST.COIL1
  N8: JP1.4, U1-RST.COIL2
  N9: JP2.2, R2.Pin_0
  N10: JP2.4, R1.Pin_0

notes:
  Use this circuit to reset/start-up the PRi after it was turned off after the last sequence. Switch into Prog mode to surpress resets that can interfere with programming.
  PRi Run/Prog Swich and Startup relay., Switch shown in Programming Mode., 2
  See schm. or PCB for layout and connections.
