# Fritzing sketch id3514_RPi_radio_0 (saved by Fritzing 0.8.7b)
breadboards: 1

parts:
  Raspberry_Pi_B_rev1 = Raspberry Pi B rev1
  S1 = Pushbutton [package="[THT]"]
  S2 = Pushbutton [package="[THT]"]
  S3 = Pushbutton [package="[THT]"]
  R1 = Resistor [tolerance=±5% resistance=220 package=THT]
  R2 = Resistor [tolerance=±5% resistance=220 package=THT]
  R3 = Resistor [tolerance=±5% resistance=220 package=THT]
  MCP3002 = IC, DIP package, 8 pins [chip_label=MCP3002]
  RE1 = Rotary Encoder [package=THT]
  R4 = Rotary Potentiometer (Small) [maximum_resistance=100kΩ package=THT]
  R5 = Rotary Potentiometer (Small) [maximum_resistance=100kΩ package=THT]

nets:
  N1: Raspberry_Pi_B_rev1.3V3, S1.Pin_3, S1.Pin_4, S2.Pin_3, S2.Pin_4, S3.Pin_3, S3.Pin_4, MCP3002.pin8, R4.leg1, R5.leg1
  N2: Raspberry_Pi_B_rev1.GND, R1.Pin_0, R2.Pin_0, R3.Pin_0, MCP3002.pin4, RE1.EncoderPinC, R4.leg2, R5.leg2
  N3: Raspberry_Pi_B_rev1.GPIO_23, S1.Pin_1, S1.Pin_2, R1.Pin_1
  N4: Raspberry_Pi_B_rev1.GPIO_17, RE1.EncoderPinA
  N5: Raspberry_Pi_B_rev1.GPIO_22, RE1.EncoderPinB
  N6: Raspberry_Pi_B_rev1.GPIO_24, S2.Pin_1, S2.Pin_2, R2.Pin_1
  N7: Raspberry_Pi_B_rev1.GPIO_10, MCP3002.pin5
  N8: Raspberry_Pi_B_rev1.GPIO_9, MCP3002.pin6
  N9: Raspberry_Pi_B_rev1.GPIO_25, S3.Pin_1, S3.Pin_2, R3.Pin_1
  N10: Raspberry_Pi_B_rev1.GPIO_11, MCP3002.pin7
  N11: Raspberry_Pi_B_rev1.GPIO_8, MCP3002.pin1
  N12: MCP3002.pin2, R5.wiper
  N13: MCP3002.pin3, R4.wiper
