# Fritzing sketch id3517_RS232_0 (saved by Fritzing 0.9.3b)
circuit board: 8.46667cm x 5.64444cm
breadboards: 1

parts:
  C1 = Electrolytic Capacitor [capacitance=10µF package="100 mil [THT, electrolytic]"]
  C3 = Electrolytic Capacitor [capacitance=10µF package="100 mil [THT, electrolytic]"]
  C5 = Electrolytic Capacitor [capacitance=10µF package="100 mil [THT, electrolytic]"]
  CN1 = DB9 right-angle female
  U1 = RS232 Transceiver [package=dil16]
  Part1 = Arduino Uno (Rev3)
  C2 = Electrolytic Capacitor [capacitance=10µF package="100 mil [THT, electrolytic]"]
  C4 = Electrolytic Capacitor [capacitance=10µF package="100 mil [THT, electrolytic]"]

nets:
  GND: C1.-, C5.+, CN1.connector4, U1.GND, Part1.GND
  VCC: C1.+, U1.VCC, Part1.5V, C4.-
  N1: C3.-, U1.C2-
  N2: C3.+, U1.C2+
  N3: C5.-, U1.V-
  N4: CN1.connector1, U1.R2IN
  N5: CN1.connector2, U1.T2OUT
  N6: U1.C1+, C2.+
  N7: U1.V+, C4.+
  N8: U1.C1-, C2.-
  N9: U1.R2OUT, Part1.D10_PWM/SS
  N10: U1.T2IN, Part1.D11_PWM/MOSI
