# Fritzing sketch id3518_RS232share_0 (saved by Fritzing 0.3.15b)
breadboards: 1

parts:
  U1 = MAX232try2
  C1 = Tantalum Capacitor [package=THT]
  C2 = Tantalum Capacitor [package=THT]
  C3 = Tantalum Capacitor [package=THT]
  C4 = Tantalum Capacitor [package=THT]
  C5 = Tantalum Capacitor [package=THT]
  J1 = female pin header, 5 pins [form="♀ (female)"]
  CN1 = DB9_rt_female

nets:
  N1: U1.connector0, C1.+
  N2: U1.connector1, C3.+
  N3: U1.connector2, C1.-
  N4: U1.connector3, C2.+
  N5: U1.connector4, C2.-
  N6: U1.connector5, C4.-
  N7: U1.connector6, CN1.connector1
  N8: U1.connector7, CN1.connector2
  N9: U1.connector8, J1.pin4
  N10: U1.connector9, J1.pin5
  N11: U1.connector14, C3.-, C4.+, C5.-, J1.pin2, CN1.connector4, CN1.connector10
  N12: U1.connector15, C5.+, J1.pin1
