# Fritzing sketch id3521_prototipo_2_0 (saved by Fritzing 0.9.3b)
circuit board: 6.34071cm x 9.06399cm
breadboards: 1

parts:
  U1 = atmega328 [package=dip]
  LED1 = LED - 5mm [color="Red (633nm)" package="5 mm [THT]"]
  Componente1 = Arduino Uno (Rev3)
  LED2 = LED - 5mm [color="Red (633nm)" package="5 mm [THT]"]
  LED3 = LED - 5mm [color="Red (633nm)" package="5 mm [THT]"]
  LED4 = LED - 5mm [color="Red (633nm)" package="5 mm [THT]"]
  LED5 = LED - 5mm [color="Red (633nm)" package="5 mm [THT]"]
  LED6 = LED - 5mm [color="Red (633nm)" package="5 mm [THT]"]
  LED7 = LED - 5mm [color="Red (633nm)" package="5 mm [THT]"]
  LED8 = LED - 5mm [color="Red (633nm)" package="5 mm [THT]"]
  LED9 = LED - 5mm [color="Red (633nm)" package="5 mm [THT]"]
  LED10 = LED - 5mm [color="Red (633nm)" package="5 mm [THT]"]
  LED12 = LED - 5mm [color="Red (633nm)" package="5 mm [THT]"]
  XTAL1 = Crystal [frequency="16 Mhz" package=THT]
  LED13 = LED - 5mm [color="Red (633nm)" package="5 mm [THT]"]
  LED14 = LED - 5mm [color="Red (633nm)" package="5 mm [THT]"]
  LED16 = LED - 5mm [color="Red (633nm)" package="5 mm [THT]"]
  LED17 = LED - 5mm [color="Red (633nm)" package="5 mm [THT]"]
  LED18 = LED - 5mm [color="Red (633nm)" package="5 mm [THT]"]
  LED20 = LED - 5mm [color="Red (633nm)" package="5 mm [THT]"]
  LED21 = LED - 5mm [color="Red (633nm)" package="5 mm [THT]"]
  LED22 = LED - 5mm [color="Red (633nm)" package="5 mm [THT]"]
  LED23 = LED - 5mm [color="Red (633nm)" package="5 mm [THT]"]
  LED24 = LED - 5mm [color="Red (633nm)" package="5 mm [THT]"]
  LED25 = LED - 5mm [color="Red (633nm)" package="5 mm [THT]"]
  LED26 = LED - 5mm [color="Red (633nm)" package="5 mm [THT]"]
  LED27 = LED - 5mm [color="Red (633nm)" package="5 mm [THT]"]
  LED28 = LED - 5mm [color="Red (633nm)" package="5 mm [THT]"]
  LED30 = LED - 5mm [color="Red (633nm)" package="5 mm [THT]"]
  LED31 = LED - 5mm [color="Red (633nm)" package="5 mm [THT]"]
  IC1 = DS1307 [package=THT]
  Y1 = CRYSTAL [package=tc26h]
  LED32 = LED - 5mm [color="Red (633nm)" package="5 mm [THT]"]
  LED11 = LED - 5mm [color="Red (633nm)" package="5 mm [THT]"]
  BAT1 = Battery Holders [package=battcom_20mm_pth]
  R4 = Resistor [tolerance=±5% resistance=220 package=THT]
  R5 = Resistor [tolerance=±5% resistance=220 package=THT]
  R6 = Resistor [tolerance=±5% resistance=220 package=THT]
  R7 = Resistor [tolerance=±5% resistance=220 package=THT]
  R8 = Resistor [tolerance=±5% resistance=220 package=THT]
  R9 = Resistor [tolerance=±5% resistance=220 package=THT]
  R10 = Resistor [tolerance=±5% resistance=220 package=THT]
  R11 = Resistor [tolerance=±5% resistance=220 package=THT]
  R12 = Resistor [tolerance=±5% resistance=220 package=THT]
  R13 = Resistor [tolerance=±5% resistance=220 package=THT]
  R14 = Resistor [tolerance=±5% resistance=220 package=THT]
  R15 = Resistor [tolerance=±5% resistance=220 package=THT]
  R16 = Resistor [tolerance=±5% resistance=220 package=THT]

nets:
  N1: U1.D0_(RX), Componente1.D2
  N2: U1.D1_(TX), LED31.anode
  N3: U1.D2, LED28.anode
  N4: U1.D3_(PWM), LED27.anode
  N5: U1.D4, LED26.anode
  VCC: U1.VCC, U1.AVCC, Componente1.VIN, IC1.+V, R13.Pin_0, R14.Pin_0, R15.Pin_0
  N6: U1.GND#7, Componente1.GND, LED13.cathode, LED14.cathode, IC1.0V, BAT1.-, R4.Pin_0, R5.Pin_1, R6.Pin_1, R9.Pin_0, R10.Pin_0, R11.Pin_0, R16.Pin_1
  N7: U1.XLAT1, XTAL1.pin_1
  N8: U1.XLAT2, XTAL1.pin_0
  N9: U1.D7, R7.Pin_0
  N10: U1.D8, R8.Pin_0
  N11: U1.D9_(PWM), LED12.anode
  N12: U1.D10_(PWM), LED11.anode
  N13: U1.D11_(PWM), LED10.anode
  N14: U1.D12, LED9.anode
  N15: U1.D13, LED8.anode
  N16: U1.GND#21, LED7.cathode
  N17: U1.A0, LED6.anode
  N18: U1.A1, LED5.anode
  N19: U1.A2, LED4.anode
  N20: U1.A3, LED3.anode
  N21: U1.A4, LED2.anode
  N22: U1.A5, LED1.anode
  N23: LED1.cathode, LED2.cathode, R10.Pin_1
  N24: Componente1.A1, R12.Pin_1
  N25: Componente1.A4/SDA, IC1.SDA_-_I2C_Data, R13.Pin_1
  N26: Componente1.A5/SCL, IC1.SCL_-_I2C_Clock, R15.Pin_1
  N27: Componente1.D8, LED18.anode
  N28: Componente1.D9_PWM, LED17.anode
  N29: Componente1.D10_PWM/SS, LED20.anode
  N30: Componente1.D11_PWM/MOSI, LED21.anode
  N31: Componente1.D12/MISO, LED22.anode
  N32: Componente1.D13/SCK, LED23.anode
  N33: Componente1.D3_PWM, R16.Pin_0
  N34: Componente1.D4, LED30.anode
  N35: Componente1.D5_PWM, LED25.anode
  N36: Componente1.D6_PWM, LED24.anode
  N37: Componente1.D7, LED16.anode
  N38: LED3.cathode, LED4.cathode
  N39: LED5.cathode, LED6.cathode
  N40: LED7.anode, R12.Pin_0
  N41: LED8.cathode, LED9.cathode, LED10.cathode
  N42: LED12.cathode, LED11.cathode, R9.Pin_1
  N43: LED13.anode, R7.Pin_1
  N44: LED14.anode, R8.Pin_1
  N45: LED16.cathode, LED18.cathode, LED24.cathode, LED25.cathode
  N46: LED17.cathode, LED20.cathode
  N47: LED21.cathode, LED22.cathode, LED23.cathode, R5.Pin_0
  N48: LED26.cathode, LED27.cathode, LED28.cathode, LED30.cathode, R6.Pin_0
  N49: LED31.cathode, R4.Pin_1
  N50: IC1.X1_-_Crystal, Y1.2
  N51: IC1.X2_-_Crystal, Y1.1
  N52: IC1.Vbat_-_Backup_Supply, BAT1.+
  N53: IC1.SWQ/OUT_-_Clock_Output, LED32.anode, R14.Pin_1
  N54: LED32.cathode, R11.Pin_1
