# Fritzing sketch id3522_RudolphSketch_0 (saved by Fritzing 0.7.11b)
breadboards: 1

parts:
  LED1 = LED - 5mm [color="Red (633nm)" package="5 mm [THT]"]
  R1 = Resistor [tolerance=±5% resistance=220 package=THT]
  GND = female pin header, 1 pin [form="♀ (female)"]
  + = female pin header, 1 pin [form="♀ (female)"]

nets:
  N1: LED1.cathode, GND.pin1
  N2: LED1.anode, R1.Pin_0
  N3: R1.Pin_1, +.pin1
