# Fritzing sketch id3524_running_led_button_fritzing_0 (saved by Fritzing 0.8.7b)
breadboards: 1

parts:
  Part1 = Arduino Uno (Rev3)
  LED2 = LED - 5mm [color="Red (633nm)" package="5 mm [THT]"]
  R1 = Resistor [tolerance=±5% resistance=220 package=THT]
  R2 = Resistor [tolerance=±5% resistance=220 package=THT]
  S1 = Pushbutton [package="[THT]"]
  R4 = Resistor [tolerance=±5% resistance=220 package=THT]
  LED3 = LED - 5mm [color="Red (633nm)" package="5 mm [THT]"]

nets:
  N1: Part1.D12/MISO, R2.Pin_0
  N2: Part1.D13/SCK, R1.Pin_0
  N3: Part1.GND, LED2.cathode, R4.Pin_0, LED3.cathode
  N4: Part1.D2, S1.Pin_3, S1.Pin_4, R4.Pin_1
  N5: Part1.5V, S1.Pin_1, S1.Pin_2
  N6: LED2.anode, R2.Pin_1
  N7: R1.Pin_1, LED3.anode
