# Fritzing sketch id3525_RunningFire_0 (saved by Fritzing 0.9.2b)
breadboards: 1

parts:
  Часть1 = Arduino Uno (Rev3)
  LED1 = LED - 5mm [color="Red (633nm)" package="5 mm [THT]"]
  R1 = Resistor [tolerance=±5% resistance=10k package=THT]
  R2 = Resistor [tolerance=±5% resistance=10k package=THT]
  LED3 = LED - 5mm [color="Red (633nm)" package="5 mm [THT]"]
  R3 = Resistor [tolerance=±5% resistance=10k package=THT]
  LED4 = LED - 5mm [color="Red (633nm)" package="5 mm [THT]"]
  R4 = Resistor [tolerance=±5% resistance=10k package=THT]
  LED5 = LED - 5mm [color="Red (633nm)" package="5 mm [THT]"]
  R5 = Resistor [tolerance=±5% resistance=10k package=THT]
  LED6 = LED - 5mm [color="Red (633nm)" package="5 mm [THT]"]
  R6 = Resistor [tolerance=±5% resistance=10k package=THT]
  LED7 = LED - 5mm [color="Red (633nm)" package="5 mm [THT]"]
  R7 = Resistor [tolerance=±5% resistance=10k package=THT]
  LED8 = LED - 5mm [color="Red (633nm)" package="5 mm [THT]"]
  R8 = Resistor [tolerance=±5% resistance=10k package=THT]
  LED9 = LED - 5mm [color="Red (633nm)" package="5 mm [THT]"]
  R9 = Resistor [tolerance=±5% resistance=220 package=THT]
  LED10 = LED - 5mm [color="Red (633nm)" package="5 mm [THT]"]

nets:
  N1: Часть1.D8, LED6.anode
  N2: Часть1.D9_PWM, LED5.anode
  N3: Часть1.D10_PWM/SS, LED4.anode
  N4: Часть1.D12/MISO, LED1.anode
  N5: Часть1.GND, R2.Pin_0, R3.Pin_0, R4.Pin_0, R5.Pin_0, R7.Pin_0, R8.Pin_0, R9.Pin_0
  N6: Часть1.D4, LED10.anode
  N7: Часть1.D5_PWM, LED9.anode
  N8: Часть1.D6_PWM, LED8.anode
  N9: Часть1.D7, LED7.anode
  N10: LED1.cathode, R1.Pin_1
  N11: R2.Pin_1, LED3.anode
  N12: R3.Pin_1, LED4.cathode
  N13: R4.Pin_1, LED5.cathode
  N14: R5.Pin_1, LED6.cathode
  N15: R6.Pin_1, LED7.cathode
  N16: R7.Pin_1, LED8.cathode
  N17: R8.Pin_1, LED9.cathode
  N18: R9.Pin_1, LED10.cathode
