# Fritzing sketch id3527_15_S4A_Educacao_0 (saved by Fritzing 0.9.3b)
circuit board: 2.96832cm x 3.62572cm
breadboards: 1

parts:
  Componente1 = Arduino Uno (Rev3)
  R1 = Photocell (LDR) [package=THT]
  R2 = Resistor [tolerance=±5% resistance=220 package="2512 [SMD]"]
  LED1 = smd LED [color="Green (555nm)" package="0805 [SMD]"]
  J1 = Basic Servo
  J2 = Basic Servo
  LED2 = smd LED [color="Yellow (595nm)" package="0805 [SMD]"]
  R4 = Resistor [tolerance=±5% resistance=220 package="2512 [SMD]"]
  LED3 = smd LED [color="Red (660nm)" package="0805 [SMD]"]
  R5 = Resistor [tolerance=±5% resistance=220 package="2512 [SMD]"]
  R6 = Resistor [tolerance=±5% resistance=220 package="2512 [SMD]"]
  S1 = Pushbutton [package="[THT]"]
  S2 = Pushbutton [package="[THT]"]
  R7 = Resistor [tolerance=±5% resistance=220 package=THT]
  R8 = Resistor [tolerance=±5% resistance=220 package=THT]
  J3 = Basic Servo
  J4 = Basic Servo
  R9 = Rotary Potentiometer (Small) [maximum_resistance=100kΩ package=THT]
  J5 = Infrared Proximity Sensor

nets:
  N1: Componente1.A0, R1.pin_0, R2.Pin_1
  N2: Componente1.A1, R9.wiper
  N3: Componente1.A2, J5.Vout
  N4: Componente1.D8, J1.pulse
  N5: Componente1.D10_PWM/SS, LED1.anode
  N6: Componente1.D11_PWM/MOSI, LED2.anode
  N7: Componente1.D12/MISO, J2.pulse
  N8: Componente1.D13/SCK, LED3.anode
  N9: Componente1.GND, R2.Pin_0, R4.Pin_0, R5.Pin_1, R7.Pin_0, R8.Pin_0, R9.leg2
  N10: Componente1.D2, S2.Pin_1
  N11: Componente1.D3_PWM, S1.Pin_1
  N12: Componente1.D4, J4.pulse
  N13: Componente1.D7, J3.pulse
  N14: Componente1.5V, R1.pin_1
  N15: LED1.cathode, R4.Pin_1
  N16: LED2.cathode, R5.Pin_0
  N17: LED3.cathode, R6.Pin_1
  N18: S1.Pin_3, S1.Pin_4, S2.Pin_3, R9.leg1

notes:
  Bracos:
  2 servos de 0-180 graus
  Rodas:
  2 servos de rotação contínua
  Esta é a pinagem para utilizar o Arduino Uno com o sistema S4A (Scratch)
  Ver na página: http://s4a.cat/
  6 Analog Inputs (A0 - A5)
  2 Digital Inputs (2, 3)
  3 Analog Outputs (PWM) (5, 6, 9)
  3 Digital Outputs (10, 11, 13)
  4 Continuous Rotation Servomotor (Outputs) (4, 7, 8, 12)
