# Fritzing sketch id3528_Theremin_0 (saved by Fritzing 0.9.2b)
breadboards: 1

parts:
  Part1 = Arduino Uno (Rev3)
  U1 = POT [package=3362u]
  R1 = Resistor [tolerance=±5% resistance=2.2k package="0402 [SMD]"]
  R2 = PHOTOCELL [package=photocell]
  R3 = Resistor [tolerance=±5% resistance=2.2k package="0402 [SMD]"]
  R4 = Basic Force Sensing Resistor (FSR) [package=THT]
  R5 = Resistor [tolerance=±5% resistance=2.2k package=THT]

nets:
  N1: Part1.A0, U1.S
  N2: Part1.A1, R2.P$1, R3.Pin_1
  N3: Part1.A2, R4.pin_1
  N4: Part1.5V, R2.P$2
  N5: Part1.GND, R3.Pin_0
  N6: U1.A, R1.Pin_1
  N7: R4.pin_0, R5.Pin_1

notes:
  Potentiometer
  signal (yellow wire) connected to A0
  Photocell
  connected to A1
  Flex Sensor
  connected to A2
  2.2K Resistors
