# Fritzing sketch id3529_Meccanoid_0 (saved by Fritzing 0.9.3b)
circuit board: 8.46667cm x 5.64444cm
breadboards: 2

parts:
  Composant1 = Arduino Uno (Rev3)
  Composant2 = HM-10
  Composant3 = Arduino Uno (Rev3)
  Power_plug1 = Power plug
  Power_plug2 = Power plug
  Composant4 = srd-05vdc-sl-c
  Composant5 = srd-05vdc-sl-c
  Composant6 = srd-05vdc-sl-c
  Composant7 = srd-05vdc-sl-c
  M1 = DC Motor
  M2 = DC Motor
  Q1 = NPN-Transistor [package="TO92 [THT]"]
  Q2 = NPN-Transistor [package="TO92 [THT]"]
  J1 = Basic Servo
  J2 = Basic Servo
  J3 = Basic Servo
  Composant8 = Arduino Esplora (Rev4)
  Composant9 = HM-10

nets:
  N1: Composant1.D8, Composant7.connector0
  N2: Composant1.D10_PWM/SS, Q1.C
  N3: Composant1.D11_PWM/MOSI, Q2.C
  GND: Composant1.GND, Composant2.connector14, Composant3.GND, Power_plug1.GND, Power_plug2.GND, Composant4.connector5, Composant5.connector5, Composant6.connector5, Composant7.connector5, Q1.E, Q2.E, J1.gnd, J2.gnd, J3.gnd
  N4: Composant1.D0/RX, Composant2.connector13, Composant3.D0/RX
  N5: Composant1.D1/TX, Composant2.connector12, Composant3.D1/TX
  N6: Composant1.D2, Composant4.connector0
  N7: Composant1.D4, Composant5.connector0
  N8: Composant1.D6_PWM, Composant6.connector0
  VIN: Composant1.VIN, Power_plug1.VCC
  N9: Composant2.connector15, Composant3.3V3
  N10: Composant3.D11_PWM/MOSI, J1.pulse
  N11: Composant3.D12/MISO, J2.pulse
  N12: Composant3.D13/SCK, J3.pulse
  VCC: Composant3.VIN, Power_plug2.VCC, Composant4.connector2, Composant5.connector2, Composant6.connector2, Composant7.connector2, J1.vcc, J2.vcc, J3.vcc
  N13: Composant4.connector3, Composant5.connector3, Q1.B
  N14: Composant4.connector4, M1.pin_2
  N15: Composant5.connector4, M1.pin_1
  N16: Composant6.connector3, Composant7.connector3, Q2.B
  N17: Composant6.connector4, M2.pin_2
  N18: Composant7.connector4, M2.pin_1
  N19: Composant8.D7/LCD_CS, Composant9.connector12
  N20: Composant8.IO8/CARD_CS, Composant9.connector13
  N21: Composant8.5V, Composant9.connector14
  N22: Composant8.GND, Composant9.connector15

notes:
  6V niMH
  ArduinoA / Relay Control
  Arduino B / Servo Control]
  HM10 / Receive Instructions via BT
  Arduino Esplora / Remote Controller
  HM10 / Send Instructions via BT
  DC Motor / Meccanoid Left Foot
  DC Motor / Meccanoid Right Foot
  SRD05VDC
  ServoMotor / Meccanoid right arm
  ServoMotor / Meccanoid left arm
  ServoMotor / Meccanoid head
  BD135
