# Fritzing sketch id352_BluetoothRobotArm_0 (saved by Fritzing 0.9.2b)
breadboards: 1

parts:
  부품1 = Arduino Uno (Rev3)
  부품2 = HC-06
  LED1 = LED - 5mm [color="Red (633nm)" package="5 mm [THT]"]
  J1 = Basic Servo
  J2 = Basic Servo

nets:
  N1: 부품1.D9_PWM, J2.pulse
  N2: 부품1.D10_PWM/SS, J1.pulse
  N3: 부품1.D11_PWM/MOSI, LED1.anode
  N4: 부품1.D2, 부품2.connector13
  N5: 부품1.D3_PWM, 부품2.connector12
  VCC: 부품1.5V, 부품2.connector15, J1.vcc, J2.vcc
  GND: 부품1.GND, 부품2.connector14, LED1.cathode, J1.gnd, J2.gnd
