# Fritzing sketch id3533_Safe_Lock_0 (saved by Fritzing 0.8.7b)
breadboards: 1

parts:
  Part1 = Arduino Uno (Rev3)
  SW1 = DIP SWITCH [package=dipswitch-02]
  SW3 = DIP SWITCH [package=dipswitch-02]
  SW4 = DIP SWITCH [package=dipswitch-02]
  R1 = Resistor [tolerance=±5% resistance=10k package="1206 [SMD]"]
  R2 = Resistor [tolerance=±5% resistance=10k package="1206 [SMD]"]
  R3 = Resistor [tolerance=±5% resistance=10k package="1206 [SMD]"]
  R4 = Resistor [tolerance=±5% resistance=10k package="1206 [SMD]"]
  R5 = Resistor [tolerance=±5% resistance=10k package="1206 [SMD]"]
  R6 = Resistor [tolerance=±5% resistance=10k package="1206 [SMD]"]
  R7 = Resistor [tolerance=±5% resistance=10k package="1206 [SMD]"]
  R8 = Resistor [tolerance=±5% resistance=10k package="1206 [SMD]"]
  SW2 = DIP SWITCH [package=dipswitch-02]
  LED1 = LED - 5mm [color="Red (633nm)" package="5 mm [THT]"]
  LED2 = LED - 5mm [color="Green (555nm)" package="5 mm [THT]"]
  R9 = Resistor [tolerance=±5% resistance=470 package=THT]
  R10 = Resistor [tolerance=±5% resistance=470 package=THT]

nets:
  N1: Part1.D8, R4.Pin_1
  N2: Part1.D9_PWM, R3.Pin_1
  N3: Part1.D10_PWM/SS, R2.Pin_1
  N4: Part1.D11_PWM/MOSI, R1.Pin_1
  N5: Part1.D2, R8.Pin_1
  N6: Part1.D3_PWM, R7.Pin_1
  N7: Part1.D4, R6.Pin_1
  N8: Part1.D5_PWM, R5.Pin_1
  N9: Part1.D6_PWM, LED1.cathode, LED1.anode, R9.Pin_1
  N10: Part1.D7, LED2.cathode, LED2.anode, R10.Pin_1
  N11: Part1.5V, SW1.1, SW1.2, SW3.1, SW3.2, SW4.1, SW4.2, SW2.1, SW2.2
  N12: Part1.GND, R1.Pin_0, R2.Pin_0, R3.Pin_0, R4.Pin_0, R5.Pin_0, R6.Pin_0, R7.Pin_0, R8.Pin_0, R9.Pin_0, R10.Pin_0
