# Fritzing sketch id3535_drum_0 (saved by Fritzing 0.9.2b)
circuit board: 8.46667cm x 5.64444cm
breadboards: 1

parts:
  R1 = Resistor [tolerance=±5% resistance=1k package="1206 [SMD]"]
  R2 = Resistor [tolerance=±5% resistance=1k package="1206 [SMD]"]
  R3 = Resistor [tolerance=±5% resistance=1k package="1206 [SMD]"]
  R4 = Resistor [tolerance=±5% resistance=1k package="1206 [SMD]"]
  R5 = Resistor [tolerance=±5% resistance=1k package="1206 [SMD]"]
  J1 = Piezo Speaker
  J2 = Piezo Speaker
  J3 = Piezo Speaker
  J4 = Piezo Speaker
  J5 = Piezo Speaker
  Part1 = Arduino Uno (Rev3)
  J6 = single row smd female pin header, 5 pins [form="♀ (female)"]

nets:
  N1: R1.Pin_0, J1.pin2, J6.pin1
  N2: R1.Pin_1, Part1.A4/SDA
  N3: R2.Pin_0, J2.pin2, J6.pin2
  N4: R2.Pin_1, Part1.A3
  N5: R3.Pin_0, J3.pin2, J6.pin3
  N6: R3.Pin_1, Part1.A2
  N7: R4.Pin_0, J4.pin2, J6.pin4
  N8: R4.Pin_1, Part1.A1
  N9: R5.Pin_0, J5.pin2, J6.pin5
  N10: R5.Pin_1, Part1.A0
  N11: J1.pin1, J2.pin1, J3.pin1, J4.pin1, J5.pin1, Part1.GND
