# Fritzing sketch id3536_salidapwm_oscila_0 (saved by Fritzing 0.9.2b)
breadboards: 1

parts:
  Parte1 = Arduino Uno (Rev3)
  LED1 = LED - 5mm [color="Red (633nm)" package="5 mm [THT]"]
  R3 = Resistor [tolerance=±5% resistance=220 package=THT]
  R4 = Trimmer Potentiometer [maximum_resistance=10kΩ package=THT]

nets:
  N1: Parte1.A0, R4.wiper
  N2: Parte1.D9_PWM, R3.Pin_1
  N3: Parte1.5V, R4.leg1
  N4: LED1.cathode, R4.leg2
  N5: LED1.anode, R3.Pin_0
