# Fritzing sketch id3538_SemaforoIntelingente_0 (saved by Fritzing 0.9.3b)
breadboards: 1

parts:
  Componente1 = Arduino Uno (Rev3)
  LED1 = LED - 5mm [color="Red (633nm)" package="5 mm [THT]"]
  LED2 = LED - 5mm [color="Yellow (595nm)" package="5 mm [THT]"]
  LED3 = LED - 5mm [color="Green (565nm)" package="5 mm [THT]"]
  R1 = Resistor [tolerance=±5% resistance=330 package=THT]
  R2 = Resistor [tolerance=±5% resistance=330 package=THT]
  R3 = Resistor [tolerance=±5% resistance=330 package=THT]
  J1 = Piezo Speaker
  R4 = Resistor [tolerance=±5% resistance=330 package=THT]

nets:
  N1: Componente1.D8, R3.Pin_0
  N2: Componente1.D12/MISO, R2.Pin_0
  N3: Componente1.D13/SCK, R1.Pin_0
  N4: Componente1.GND, LED1.cathode, LED2.cathode, LED3.cathode, J1.pin1
  N5: Componente1.D4, R4.Pin_0
  N6: LED1.anode, R1.Pin_1
  N7: LED2.anode, R2.Pin_1
  N8: LED3.anode, R3.Pin_1
  N9: J1.pin2, R4.Pin_1
