# Fritzing sketch id3539_sample1_0 (saved by Fritzing 0.9.3b)
circuit board: 8.47cm x 5.64444cm
breadboards: 1

parts:
  S1 = Pushbutton [package="[THT]"]
  パーツ1 = Arduino Uno (Rev3)
  LED1 = LED - 5mm [color="Green (555nm)" package="5 mm [THT]"]
  R1 = Resistor [tolerance=±5% resistance=220 package=THT]
  R2 = Resistor [tolerance=±5% resistance=10k package="0402 [SMD]"]

nets:
  N1: S1.Pin_1, S1.Pin_2, パーツ1.D7, R2.Pin_0
  N2: S1.Pin_3, S1.Pin_4, パーツ1.5V
  N3: パーツ1.D9_PWM, LED1.cathode
  N4: パーツ1.GND, R1.Pin_1, R2.Pin_1
  N5: LED1.anode, R1.Pin_0
