# Fritzing sketch id353_AppEE_Hardware_0 (saved by Fritzing 0.9.2b)
circuit board: 8.46667cm x 5.64444cm
breadboards: 1

parts:
  Parte1 = Arduino Yun
  Grove1 = Grove Light Sensor
  Lhi1 = LHi958 [package=to-39]
  U1 = Voltage Regulator - 5V [package="TO220 [THT]"]
  VCC1 = Battery block 9V
  LED1 = smd LED [color="Red (633nm)" package="0805 [SMD]"]

nets:
  N1: Parte1.A0, Grove1.SIG
  N2: Parte1.D6_PWM, LED1.anode
  N3: Parte1.D7, Lhi1.S
  5V: Parte1.5V, Grove1.VCC, Lhi1.D, U1.output_voltage
  GND: Parte1.GND, Grove1.GND, Lhi1.GND, U1.GND, VCC1.-, LED1.cathode
  N4: U1.input_voltage, VCC1.+
