# Fritzing sketch id3540_Sensor_Workshop_board_layout_0 (saved by Fritzing 0.9.2b)
breadboards: 1

parts:
  R1 = PHOTOCELL [package=photocell]
  R2 = PHOTOCELL [package=photocell]
  R3 = PHOTOCELL [package=photocell]
  R4 = PHOTOCELL [package=photocell]
  R5 = PHOTOCELL [package=photocell]
  R6 = PHOTOCELL [package=photocell]
  R7 = Resistor [tolerance=±5% resistance=220 package=THT]
  LED2 = LED - 3mm [color="Red (633nm)" package="3 mm [THT]"]
  R8 = Resistor [tolerance=±5% resistance=220 package=THT]
  LED3 = LED - 3mm [color="Red (633nm)" package="3 mm [THT]"]
  R9 = Resistor [tolerance=±5% resistance=220 package=THT]
  LED4 = LED - 3mm [color="Red (633nm)" package="3 mm [THT]"]
  R10 = Resistor [tolerance=±5% resistance=220 package=THT]
  LED5 = LED - 3mm [color="Red (633nm)" package="3 mm [THT]"]
  R11 = Resistor [tolerance=±5% resistance=220 package=THT]
  LED6 = LED - 3mm [color="Red (633nm)" package="3 mm [THT]"]
  R12 = Resistor [tolerance=±5% resistance=220 package=THT]
  LED7 = LED - 3mm [color="Red (633nm)" package="3 mm [THT]"]
  Part1 = Arduino Uno (Rev3) - ICSP
  R13 = Resistor [tolerance=±5% resistance=220 package=THT]
  R14 = Resistor [tolerance=±5% resistance=220 package=THT]  # not connected
  R15 = Resistor [tolerance=±5% resistance=220 package=THT]
  R16 = Resistor [tolerance=±5% resistance=220 package=THT]
  R17 = Resistor [tolerance=±5% resistance=220 package=THT]
  R18 = Resistor [tolerance=±5% resistance=220 package=THT]
  R19 = Resistor [tolerance=±5% resistance=220 package=THT]

nets:
  N1: R1.P$1, R1.P$2, R2.P$1, R3.P$1, R4.P$1, R5.P$1, R6.P$1, Part1.5V
  N2: R2.P$2, Part1.A3, R17.Pin_0
  N3: R3.P$2, Part1.A0, R13.Pin_0
  N4: R4.P$2, Part1.A4/SDA, R18.Pin_0
  N5: R5.P$2, Part1.A1, R15.Pin_0
  N6: R6.P$2, Part1.A2, R16.Pin_0
  N7: R7.Pin_0, R7.Pin_1, LED2.cathode, Part1.D11_PWM/MOSI
  N8: LED2.anode, LED3.anode, LED4.anode, LED5.anode, LED6.anode, LED7.anode, Part1.GND, R13.Pin_1, R15.Pin_1, R16.Pin_1, R17.Pin_1, R18.Pin_1, R19.Pin_1
  N9: R8.Pin_0, R8.Pin_1, LED3.cathode, Part1.D10_PWM/SS
  N10: R9.Pin_0, R9.Pin_1, LED4.cathode, Part1.D9_PWM
  N11: R10.Pin_0, R10.Pin_1, LED5.cathode, Part1.D6_PWM
  N12: R11.Pin_0, R11.Pin_1, LED6.cathode, Part1.D5_PWM
  N13: R12.Pin_0, R12.Pin_1, LED7.cathode, Part1.D3_PWM
  N14: Part1.A5/SCL, R19.Pin_0
