# Fritzing sketch id3541_sbls_0 (saved by Fritzing 0.9.3b)
breadboards: 1

parts:
  Flex_Sensor = Basic Flex Resistor
  Accelerometer = ADXL335 [package=lfcsp-16]
  MCU = Photon
  Power_Supply = prefix0000

nets:
  N1: Flex_Sensor.Pin_2, Accelerometer.VS, MCU.3V3
  N2: Flex_Sensor.pin_1, Accelerometer.COM, MCU.A3, MCU.GND, Power_Supply.connector29
  N3: Accelerometer.ZOUT, MCU.A2
  N4: Accelerometer.YOUT, MCU.A1
  N5: Accelerometer.XOUT, MCU.A0
  N6: MCU.VIN, Power_Supply.connector27
