# Fritzing sketch id3543_scalextric_0 (saved by Fritzing 0.6.5b)
breadboards: 1

parts:
  Arduino1 = Arduino
  VCC1 = 4 x AAA Battery Mount
  C2 = Tantalum Capacitor [capacitance="1 μF" voltage=16V package="100 mil [THT, tantalum]"]
  Q1 = Basic FET P-Channel [part_number=TIP120 package="TO220 [THT]"]
  R4 = Resistor [tolerance=±5% resistance=1.5k package=THT]
  M1 = DC Motor
  D4 = Rectifier Diode [part_number=1N4001 package="300 mil [THT]"]
  R7 = Big Potentiometer [part_number="60 (power throttle)"]
  R8 = Resistor [tolerance=±5% resistance=68 package=THT]

nets:
  GND: Arduino1.GND, C2.-, Q1.source, R8.Pin_1
  N1: Arduino1.D9, R4.Pin_0
  N2: Arduino1.+5V, R7.connector0
  5V: Arduino1.VIN, VCC1.+, M1.pin_2, D4.cathode
  N3: Arduino1.A0, C2.+, R7.connector1, R7.connector2, R8.Pin_0
  N4: Q1.gate, R4.Pin_1
  N5: Q1.drain, M1.pin_1, D4.anode

notes:
  Ardulextric
