# Fritzing sketch id3544_FRITZING_CKT_0 (saved by Fritzing 0.9.3b)
circuit board: 8.46667cm x 5.64444cm
breadboards: 1

parts:
  Part1 = Arduino Uno (Rev3) - ICSP
  IC1 = ULN2003A [package="DIP16 [THT]"]
  M1 = Stepper Motor - Unipolar
  VCC2 = Battery
  VCC1 = Battery block 9V
  LD1 = b-tz.com

nets:
  N1: Part1.ICSP_MOSI, Part1.D11_PWM/MOSI, IC1.In_4
  N2: Part1.5V, LD1.connector1
  N3: Part1.D8, IC1.In_1
  N4: Part1.D9_PWM, IC1.In_2
  N5: Part1.D10_PWM/SS, IC1.In_3
  N6: Part1.GND, IC1.0V, VCC1.-, LD1.connector0
  N7: IC1.COM_-_Common, M1.COMMON_1, M1.COMMON_2, VCC2.+
  N8: IC1.Out_4, M1.D
  N9: IC1.Out_3, M1.B
  N10: IC1.Out_2, M1.C
  N11: IC1.Out_1, M1.A
  N12: VCC2.-, VCC1.+
