# Fritzing sketch id3545_circuito_(1)_0 (saved by Fritzing 0.9.3b)
breadboards: 1

parts:
  Componente1 = Arduino Uno (Rev3)
  R1 = Photocell (LDR) [package=THT]
  RHT1 = Humidity and Temperature Sensor RHT03
  PIR2 = PIR_sensor
  R2 = Resistor [tolerance=±5% resistance=220 package=THT]

nets:
  N1: Componente1.A0, RHT1.Data-signal
  N2: Componente1.A2, R1.pin_1, R2.Pin_0
  N3: Componente1.D9_PWM, PIR2.connector2
  5V: Componente1.5V, R1.pin_0, RHT1.Vcc, PIR2.connector1
  N4: Componente1.GND, RHT1.GND_1, PIR2.connector3, R2.Pin_1
