# Fritzing sketch id3547_Schakel_Lichtkast_0 (saved by Fritzing 0.9.0b)
breadboards: 1

parts:
  Sleutel_1 = Round Pushbutton
  S1 = Round Pushbutton
  S2 = Round Pushbutton
  S3 = Round Pushbutton
  S4 = Round Pushbutton
  App_2 = DC Motor
  App_1 = DC Motor
  App_3 = DC Motor
  App_4 = DC Motor
  Evt_Zekering_A = FUSE [package=fuse_5mm]

nets:
  N1: Sleutel_1.leg0, S1.leg0, S2.leg0, S3.leg1, S4.leg1
  N2: Sleutel_1.leg1, Evt_Zekering_A.1
  N3: S1.leg1, App_2.pin_1
  N4: S2.leg1, App_1.pin_1
  N5: S3.leg0, App_3.pin_1
  N6: S4.leg0, App_4.pin_1
  220V/Kijken welk Amp. geschikt is: App_2.pin_2, App_1.pin_2, App_3.pin_2, App_4.pin_2, Evt_Zekering_A.2

notes:
  Stekkerdoos
