# Fritzing sketch id3548_schele_mixer2_0 (saved by Fritzing 0.7.4b)
breadboards: 1

parts:
  Part1 = SPDT-tact-small
  R1 = Big Potentiometer
  T1 = NPN-Transistor [package="TO92 [THT]"]
  T1_2 = NPN-Transistor [package="TO92 [THT]"]
  VR = NPN-Transistor [package="TO92 [THT]"]
  1881 = PICAXE-08 [package=THT]
  1k = Resistor [tolerance=±5% resistance=220 package=THT]
  2_2k = Resistor [tolerance=±5% resistance=220 package=THT]
  470 = Resistor [tolerance=±5% resistance=220 package=THT]
  75 = Resistor [tolerance=±5% resistance=220 package=THT]
  470_2 = Resistor [tolerance=±5% resistance=220 package=THT]
  470_3 = Resistor [tolerance=±5% resistance=220 package=THT]
  T2 = NPN-Transistor [package="TO92 [THT]"]
  47uf = Electrolytic Capacitor [capacitance=1µF package="100 mil [THT, electrolytic]"]
  104 = ceramic capacitor
  104_2 = ceramic capacitor
  680k = Resistor [tolerance=±5% resistance=220 package=THT]
  47uf_2 = Electrolytic Capacitor [capacitance=1µF package="100 mil [THT, electrolytic]"]
  47uf1 = Electrolytic Capacitor [capacitance=1µF package="100 mil [THT, electrolytic]"]
  47uf_3 = Electrolytic Capacitor [capacitance=1µF package="100 mil [THT, electrolytic]"]
  D1 = Rectifier Diode [part_number=1N4001 package="300 mil [THT]"]
  DIP = IC, DIP package, 6 pins [chip_label=IC spacing=300mil]
  Part2 = rca_jack_silver
  Part3 = rca_jack_silver
  Part4 = rca_jack_silver
  75_2 = Resistor [tolerance=±5% resistance=220 package=THT]
  20k = Resistor [tolerance=±5% resistance=220 package=THT]
  10k = Resistor [tolerance=±5% resistance=220 package=THT]
  1k_2 = Resistor [tolerance=±5% resistance=220 package=THT]
  102 = ceramic capacitor
  103 = ceramic capacitor
  223 = ceramic capacitor
  20k_2 = Resistor [tolerance=±5% resistance=220 package=THT]
  47uf2 = Electrolytic Capacitor [capacitance=1µF package="100 mil [THT, electrolytic]"]
  small_signal_diode1 = small signal diode
  120 = Resistor [tolerance=±5% resistance=220 package=THT]
  75_3 = Resistor [tolerance=±5% resistance=220 package=THT]
  20k_3 = Resistor [tolerance=±5% resistance=220 package=THT]
  - = header hole
  + = header hole
  104_3 = ceramic capacitor
  hole1 = header hole
  hole2 = header hole
  hole3 = header hole
  R2 = resistor
  LED1 = LED - 3mm [color="Red (633nm)" package="3 mm [THT]"]

nets:
  N1: Part1.connector0, Part1.connector4, VR.B, 1881.In_3, 1k.Pin_0, 470.Pin_0, 104_2.connector1, 680k.Pin_0, 47uf1.-, 47uf_3.-, Part2.connector0, Part2.connector2, Part3.connector0, Part3.connector2, Part4.connector2, 10k.Pin_0, 102.connector1, 103.connector1, 223.connector1, -.connector0, 104_3.connector0, R2.connector0
  N2: Part1.connector1, 47uf_2.-, Part2.connector1
  N3: Part1.connector2, 104.connector1
  N4: Part1.connector3, 47uf.-, Part3.connector1
  N5: R1.connector2, 47uf.+
  N6: R1.connector3, 1k_2.Pin_1
  N7: R1.connector4, 47uf_2.+
  N8: T1.E, 470.Pin_1, 470_3.Pin_0
  N9: T1.B, 1k.Pin_1, 2_2k.Pin_1, 47uf2.-, small_signal_diode1.connector0
  N10: T1.C, 470_2.Pin_1, T2.B
  N11: T1_2.E, DIP.pin4, DIP.pin5, DIP.pin6, 10k.Pin_1, 120.Pin_1
  N12: T1_2.B, 20k.Pin_1, 1k_2.Pin_0
  N13: T1_2.C, VR.E, 1881.0V, 2_2k.Pin_0, 75.Pin_0, 470_2.Pin_0, 47uf1.+, 20k.Pin_0, 20k_2.Pin_1, 104_3.connector1
  N14: VR.C, 47uf_3.+, D1.cathode, LED1.anode
  N15: 1881.+V, 75_3.Pin_1
  N16: 1881.Serial_In, 104.connector0
  N17: 1881.In/Out_2, 20k_3.Pin_1
  N18: 1881.In/Out_1, 104_2.connector0, 680k.Pin_1
  N19: 75.Pin_1, T2.E
  N20: 470_3.Pin_1, T2.C, 75_2.Pin_1
  N21: D1.anode, hole1.connector0, hole2.connector0
  N22: DIP.pin1, 102.connector0
  N23: DIP.pin2, 103.connector0
  N24: DIP.pin3, 223.connector0
  N25: Part4.connector1, 75_2.Pin_0
  N26: 20k_2.Pin_0, small_signal_diode1.connector1
  N27: 47uf2.+, 120.Pin_0, 75_3.Pin_0, 20k_3.Pin_0
  N28: +.connector0, hole3.connector0
  N29: R2.connector1, LED1.cathode

notes:
  gieskes
  1881
