# Fritzing sketch id3549_schema_electrique_0 (saved by Fritzing 0.9.2b)
breadboards: 1

parts:
  Part1 = Arduino Uno (Rev3) - ICSP
  J1 = Basic Servo
  J2 = Basic Servo
  J3 = Basic Servo
  J4 = Basic Servo

nets:
  N1: Part1.D10_PWM/SS, J2.pulse
  N2: Part1.D11_PWM/MOSI, J3.pulse
  N3: Part1.D3_PWM, J4.pulse
  N4: Part1.D5_PWM, J1.pulse
  VCC: Part1.5V, J1.vcc, J2.vcc, J3.vcc, J4.vcc
  GND: Part1.GND, J1.gnd, J2.gnd, J3.gnd, J4.gnd
