# Fritzing sketch id3550_The_Best_Schematic_for_Culminating_0 (saved by Fritzing 0.9.3b)

parts:
  Part1 = Arduino Uno (Rev3)
  LCD1 = LCD screen
  S1 = Momentary Switch [package=ksa_sealed_tac_switch]
  S2 = Momentary Switch [package=ksa_sealed_tac_switch]
  S3 = Momentary Switch [package=ksa_sealed_tac_switch]
  S4 = Momentary Switch [package=ksa_sealed_tac_switch]
  R1 = Resistor [tolerance=±5% resistance=1k package="0805 [SMD]"]
  R2 = Resistor [tolerance=±5% resistance=1k package="0805 [SMD]"]
  R3 = Resistor [tolerance=±5% resistance=1k package="0805 [SMD]"]
  R4 = Resistor [tolerance=±5% resistance=1k package="0805 [SMD]"]
  S5 = Momentary Switch [package=ksa_sealed_tac_switch]
  R5 = Resistor [tolerance=±5% resistance=1k package="0805 [SMD]"]

nets:
  N1: Part1.A0, S2.3
  N2: Part1.A1, S4.3
  N3: Part1.A2, S3.3
  N4: Part1.A3, S1.3
  N5: Part1.D11_PWM/MOSI, LCD1.E
  N6: Part1.D12/MISO, LCD1.RS
  N7: Part1.D2, LCD1.DB7
  N8: Part1.D3_PWM, LCD1.DB6
  N9: Part1.D4, LCD1.DB5
  N10: Part1.D5_PWM, LCD1.DB4
  N11: Part1.D6_PWM, S5.3
  5V: Part1.5V, LCD1.VDD, LCD1.LED+, S1.2, S2.2, S3.2, S4.2, S5.2
  GND: Part1.GND, LCD1.VSS, LCD1.V0, LCD1.R/W, LCD1.LED-, R1.Pin_0, R2.Pin_0, R3.Pin_0, R4.Pin_0, R5.Pin_0
  N12: S1.4, R2.Pin_1
  N13: S2.4, R4.Pin_1
  N14: S3.4, R1.Pin_1
  N15: S4.4, R3.Pin_1
  N16: S5.4, R5.Pin_1
