# Fritzing sketch id3551_Schematic_0 (saved by Fritzing 0.9.2b)
breadboards: 1

parts:
  Part1 = Arduino Uno (Rev3)
  Part2 = Real Time Clock Module - DS1307 RTC Breakout Board
  R1 = Resistor [tolerance=±5% resistance=220 package=THT]
  R2 = Resistor [tolerance=±5% resistance=220 package=THT]
  R3 = Photocell (LDR) [package=THT]
  R4 = Photocell (LDR) [package=THT]
  R5 = Resistor [tolerance=±5% resistance=220 package=THT]
  R6 = Resistor [tolerance=±5% resistance=220 package=THT]
  Part3 = Arduino Color LCD Shield  # not connected
  Part4 = ACS712 Low Current Sensor Board v12
  J1 = Basic Servo
  J2 = Basic Servo
  R7 = Resistor [tolerance=±5% resistance=220 package=THT]
  VCC1 = Battery

nets:
  N1: Part1.A0, R6.Pin_0
  N2: Part1.A1, R5.Pin_1
  N3: Part1.A3, Part4.VO
  N4: Part1.A4/SDA, Part2.SDA, R1.Pin_1
  N5: Part1.A5/SCL, Part2.SCL
  N6: Part1.D9_PWM, J2.pulse
  N7: Part1.D6_PWM, J1.pulse
  5V: Part1.5V, Part2.5V, R1.Pin_0, R2.Pin_0, R3.pin_0, R4.pin_1, Part4.5V, J1.vcc, J2.vcc, VCC1.-
  GND: Part1.GND, Part2.GND, R5.Pin_0, R6.Pin_1, J1.gnd, J2.gnd, R7.Pin_1, VCC1.+
  N8: Part4.GND, R7.Pin_0

notes:
  This is supposed to be a half breadboard
  4 AA Batteries
  6 Volts
  These two photosensors ride on the sides of the solar panel
  Two Vigor VS 2A Servo motors, 5kgf-cm @6v
  "Solar Panel"
  (Actually Arduino LED Shield)
