# Fritzing sketch id3552_Arduino_0 (saved by Fritzing 0.9.3b)
circuit board: 6cm x 4.8cm
breadboards: 1

parts:
  U1 = atmega328 [package=dip]
  J3 = female pin header, 2 pins [form="♀ (female)"]
  J4 = female pin header, 2 pins [form="♀ (female)"]
  J5 = female pin header, 2 pins [form="♀ (female)"]
  J6 = female pin header, 2 pins [form="♀ (female)"]
  J8 = female pin header, 2 pins [form="♀ (female)"]
  J9 = female pin header, 2 pins [form="♀ (female)"]
  J13 = female pin header, 2 pins [form="♀ (female)"]
  J14 = female pin header, 2 pins [form="♀ (female)"]
  J15 = female pin header, 2 pins [form="♀ (female)"]
  J16 = female pin header, 2 pins [form="♀ (female)"]
  J18 = female pin header, 2 pins [form="♀ (female)"]
  J19 = female pin header, 2 pins [form="♀ (female)"]
  J20 = female pin header, 2 pins [form="♀ (female)"]
  J21 = female pin header, 2 pins [form="♀ (female)"]
  J22 = female pin header, 2 pins [form="♀ (female)"]
  C2 = Ceramic Capacitor [capacitance="100 nF" package="100 mil [THT, multilayer]"]
  C1 = Ceramic Capacitor [capacitance="100 nF" package="100 mil [THT, multilayer]"]
  IC1 = Voltage Regulator [package=to220-igo]
  S1 = Pushbutton [package="[THT]"]
  J23 = Screw terminal - 2 pins [package=THT]
  R2 = Resistor [tolerance=±5% resistance=220 package=THT]
  LED1 = LED - 5mm [color="Red (633nm)" package="5 mm [THT]"]
  LED2 = LED - 5mm [color="Red (633nm)" package="5 mm [THT]"]
  R3 = Resistor [tolerance=±5% resistance=220 package=THT]
  J24 = Screw terminal - 2 pins [package=THT]
  J1 = female pin header, 2 pins [form="♀ (female)"]
  Y1 = CRYSTAL [package=hc49us]
  J2 = female pin header, 2 pins [form="♀ (female)"]

nets:
  N1: U1.RESET, J3.pin2, J15.pin1, S1.Pin_1, S1.Pin_2, LED1.cathode
  N2: U1.D0_(RX), J6.pin1, J2.pin2
  N3: U1.D1_(TX), J3.pin1, J6.pin2
  N4: U1.D2, J5.pin1
  N5: U1.D3_(PWM), J5.pin2
  N6: U1.D4, J18.pin1
  N7: U1.VCC, U1.AVCC, J4.pin1, IC1.OUT, R2.Pin_0, R3.Pin_0, J24.pin1, J2.pin1
  GND: U1.GND, J4.pin2, J8.pin2, J16.pin1, C2.1, C1.0, IC1.GND, S1.Pin_3, S1.Pin_4, J23.pin2, J24.pin2, J1.pin1
  N8: U1.XLAT1, C1.1, Y1.1
  N9: U1.XLAT2, C2.0, Y1.2
  N10: U1.D5_(PWM), J18.pin2
  N11: U1.D6_(PWM), J19.pin1
  N12: U1.D7, J19.pin2
  N13: U1.D8, J20.pin1
  N14: U1.D9_(PWM), J20.pin2
  N15: U1.D10_(PWM), J21.pin1
  N16: U1.D11_(PWM), J21.pin2
  N17: U1.D12, J9.pin1
  N18: U1.D13, J9.pin2, LED2.cathode
  N19: U1.AREF, J8.pin1
  N20: U1.A0, J14.pin1
  N21: U1.A1, J14.pin2
  N22: U1.A2, J13.pin1
  N23: U1.A3, J13.pin2
  N24: U1.A4, J22.pin1
  N25: U1.A5, J22.pin2
  N26: IC1.IN, J23.pin1
  N27: R2.Pin_1, LED1.anode
  N28: LED2.anode, R3.Pin_1

notes:
  Programador FTDI
  A0-->A5
  ISDR
