# Fritzing sketch id3554_Untitled_Sketch_0 (saved by Fritzing 0.9.3b)
breadboards: 1

parts:
  Part1 = Arduino Uno (Rev3)
  LED1 = RGB LED (com. anode, rbg) [package="5 mm [THT]"]
  R1 = Resistor [tolerance=±5% resistance=220 package=THT]
  R2 = Resistor [tolerance=±5% resistance=220 package=THT]
  R3 = Resistor [tolerance=±5% resistance=220 package=THT]
  R4 = Resistor [tolerance=±5% resistance=220 package=THT]
  R5 = Resistor [tolerance=±5% resistance=220 package=THT]
  S3 = Pushbutton [package="[SMD]"]
  S4 = Pushbutton [package="[SMD]"]
  VCC1 = Battery block 9V  # not connected

nets:
  N1: Part1.D8, S3.Pin_3, S3.Pin_4
  N2: Part1.D2, R2.Pin_0
  N3: Part1.D3_PWM, R5.Pin_1
  N4: Part1.D4, R1.Pin_1
  N5: Part1.D7, R3.Pin_1, S4.Pin_3, S4.Pin_4
  N6: Part1.5V, S3.Pin_1, S3.Pin_2, S4.Pin_1, S4.Pin_2
  N7: Part1.GND, LED1.common_anode, R3.Pin_0, R4.Pin_0
  N8: LED1.red_cathode, R2.Pin_1
  N9: LED1.blue_cathode, R5.Pin_0
  N10: LED1.green_cathode, R1.Pin_0

notes:
  HI LOL
