# Fritzing sketch id3555_Schaltplan_Schule_0 (saved by Fritzing 0.9.3b)
breadboards: 1

parts:
  Bauteil1 = Arduino Uno (Rev3)
  SPKR1 = Loudspeaker
  S1 = Pushbutton [package="[THT]"]
  S2 = Pushbutton [package="[THT]"]
  S3 = Pushbutton [package="[THT]"]
  S4 = Pushbutton [package="[THT]"]
  S5 = Pushbutton [package="[THT]"]
  S6 = Pushbutton [package="[THT]"]
  S7 = Pushbutton [package="[THT]"]
  S8 = Pushbutton [package="[THT]"]

nets:
  N1: Bauteil1.A1, S7.Pin_1, S7.Pin_2
  N2: Bauteil1.A2, S8.Pin_1, S8.Pin_2
  N3: Bauteil1.D9_PWM, S3.Pin_1, S3.Pin_2
  N4: Bauteil1.D10_PWM/SS, S4.Pin_1, S4.Pin_2
  N5: Bauteil1.D11_PWM/MOSI, S5.Pin_1, S5.Pin_2
  N6: Bauteil1.GND, SPKR1.pin1, S1.Pin_3, S1.Pin_4, S2.Pin_3, S2.Pin_4, S3.Pin_3, S3.Pin_4, S4.Pin_3, S4.Pin_4, S5.Pin_3, S5.Pin_4, S6.Pin_3, S6.Pin_4, S7.Pin_3, S7.Pin_4, S8.Pin_3, S8.Pin_4
  N7: Bauteil1.D3_PWM, SPKR1.pin2
  N8: Bauteil1.D5_PWM, S1.Pin_1, S1.Pin_2
  N9: Bauteil1.D6_PWM, S2.Pin_1, S2.Pin_2
  N10: S6.Pin_1, S6.Pin_2
