# Fritzing sketch id3556_ScoreKeeper_0 (saved by Fritzing 0.9.2b)
breadboards: 1

parts:
  S1 = Pushbutton [package="[THT]"]
  LCD1 = LCD screen
  S2 = Pushbutton [package="[THT]"]
  S3 = Pushbutton [package="[THT]"]
  S4 = Pushbutton [package="[THT]"]
  R1 = Rotary Potentiometer (Small) [maximum_resistance=100kΩ package=THT]
  Part1 = Arduino Uno (Rev3)
  R2 = Resistor [tolerance=±5% resistance=220 package=THT]
  R3 = Resistor [tolerance=±5% resistance=10k package=THT]
  R4 = Resistor [tolerance=±5% resistance=10k package=THT]
  R5 = Resistor [tolerance=±5% resistance=10k package=THT]
  R6 = Resistor [tolerance=±5% resistance=10k package=THT]

nets (from the schematic view):
  N1: S1.Pin_1, S1.Pin_2, S2.Pin_1, S2.Pin_2, S3.Pin_1, S3.Pin_2, S4.Pin_1, S4.Pin_2, R1.leg2, R2.Pin_0
  N2: S1.Pin_3, S1.Pin_4
  N3: LCD1.VSS, LCD1.R/W, LCD1.LED-
  N4: LCD1.V0, R1.wiper
  N5: LCD1.RS, Part1.D12/MISO
  N6: LCD1.E, Part1.D11_PWM/MOSI
  N7: LCD1.DB4, Part1.D5_PWM
  N8: LCD1.DB5, Part1.D4
  N9: LCD1.DB6, Part1.D3_PWM
  N10: LCD1.DB7, Part1.D2
  N11: LCD1.LED+, R2.Pin_1
  N12: S2.Pin_3, S2.Pin_4, Part1.D9_PWM, R4.Pin_1
  N13: S3.Pin_3, S3.Pin_4
  N14: S4.Pin_3, S4.Pin_4
  N15: R1.leg1, Part1.GND, R3.Pin_0
  N16: R4.Pin_0, R5.Pin_0, R6.Pin_0
