# Fritzing sketch id3557_ScratchGPIO_0 (saved by Fritzing 0.9.2b)
breadboards: 1

parts:
  Raspberry_Pi1 = Raspberry Pi 2
  LED1 = LED - 5mm [color="Red (633nm)" package="5 mm [THT]"]
  R1 = Resistor [tolerance=±5% resistance=220 package=THT]
  S1 = Pushbutton [package="[THT]"]

nets:
  N1: Raspberry_Pi1.3V3, S1.Pin_3, S1.Pin_4
  N2: Raspberry_Pi1.GPIO10, S1.Pin_1, S1.Pin_2
  N3: Raspberry_Pi1.GPIO18, LED1.anode
  N4: Raspberry_Pi1.GND, R1.Pin_1
  N5: LED1.cathode, R1.Pin_0
