# Fritzing sketch id3558_flowerpot_0 (saved by Fritzing 0.9.2b)

parts:
  부품1 = Arduino Uno (Rev3)
  부품2 = Humidity Sensor - HIH-4030 Breakout

nets:
  N1: 부품1.A0, 부품2.OUT
  5V: 부품1.5V, 부품2.VCC
  GND: 부품1.GND, 부품2.GND
