# Fritzing sketch id3559_hand_0 (saved by Fritzing 0.9.2b)
breadboards: 1

parts:
  부품1 = Arduino Uno (Rev3)
  R1 = Resistor [tolerance=±5% resistance=10k package=THT]
  R2 = Basic Flex Resistor

nets:
  N1: 부품1.A0, R1.Pin_1, R2.pin_1
  N2: 부품1.GND, R1.Pin_0
  N3: 부품1.5V, R2.Pin_2
