# Fritzing sketch id355_Analog_Magnet_finder_Breadboard_&_Diagram (saved by Fritzing 0.3.12b)
breadboards: 1

parts:
  VCC1 = obsolete Battery
  DI1 = 7-Segment LED Display [package=THT]
  S1 = Reed switch [package=THT]
  S2 = Reed switch [package=THT]
  S3 = Reed switch [package=THT]
  S4 = Toggle Switch [package=THT]
  LED1 = Red LED - 5mm

nets:
  N1: VCC1.-, S1.pin_1, S2.pin_1, S3.pin_1
  N2: VCC1.+, DI1.commAnode#7, S4.COM, S4.L2, LED1.cathode, LED1.anode
  N3: DI1.cathodeE, DI1.cathodeF, S1.pin_2
  N4: DI1.cathodeC, DI1.cathodeB, S3.pin_2
  N5: DI1.cathodeA, S2.pin_2
