# Fritzing sketch id355_Aprinderea_unui_LED_direct_de_la_sursa_0 (saved by Fritzing 0.9.3b)
breadboards: 1

parts:
  D1 = LTE-302 [package=lte-302]
  R1 = Resistor [tolerance=±5% resistance=1.6k package=THT]
  V1 = DC Power [voltage=5]

nets (from the schematic view):
  N1: D1.A, V1.V+
  N2: D1.C, R1.Pin_0
  GND: R1.Pin_1, V1.V-
