# Fritzing sketch id3560_Mini_Streetlamp_0 (saved by Fritzing 0.9.2b)
breadboards: 1

parts:
  부품1 = Arduino Uno (Rev3)
  R1 = Resistor [tolerance=±5% resistance=220 package=THT]
  LED1 = LED - 5mm [color="Red (633nm)" package="5 mm [THT]"]
  R2 = Photocell (LDR) [package=THT]
  R3 = Resistor [tolerance=±5% resistance=10k package=THT]

nets:
  N1: 부품1.A0, R2.pin_0, R3.Pin_1
  N2: 부품1.D11_PWM/MOSI, LED1.anode
  N3: 부품1.GND, R1.Pin_0, R3.Pin_0
  N4: 부품1.5V, R2.pin_1
  N5: R1.Pin_1, LED1.cathode
