# Fritzing sketch id3561_mole_0 (saved by Fritzing 0.9.2b)
breadboards: 1

parts:
  부품1 = Arduino Uno (Rev3)
  R1 = Resistor [tolerance=±5% resistance=10k package=THT]
  J1 = Basic Force Sensing Resistor (FSR) [package=THT]

nets:
  N1: 부품1.A0, R1.Pin_1, J1.pin_0
  N2: 부품1.GND, R1.Pin_0
  N3: 부품1.5V, J1.pin_1
