# Fritzing sketch id3562_rgb_led_0 (saved by Fritzing 0.9.2b)

parts:
  부품1 = Arduino Uno (Rev3)
  LED1 = RGB LED (com. anode, rbg) [package="5 mm [THT]"]

nets:
  N1: 부품1.D9_PWM, LED1.blue_cathode
  N2: 부품1.D10_PWM/SS, LED1.green_cathode
  N3: 부품1.D11_PWM/MOSI, LED1.red_cathode
  N4: 부품1.GND, LED1.common_anode
