# Fritzing sketch id3567_Test_1602_Parallel_0 (saved by Fritzing 0.9.2b)

parts:
  LCD1 = LCD screen
  Onderdeel1 = Arduino Uno (Rev3)
  R1 = TRIMPOT [package=trimpot_pth_s3_lock]

nets:
  N1: LCD1.VSS, R1.CCW
  VDD: LCD1.VDD, Onderdeel1.5V
  N2: LCD1.V0, R1.WIPER
  N3: LCD1.RS, Onderdeel1.D2
  N4: LCD1.E, Onderdeel1.D4
  N5: LCD1.DB4, Onderdeel1.D8
  N6: LCD1.DB5, Onderdeel1.D9_PWM
  N7: LCD1.DB6, Onderdeel1.D10_PWM/SS
  N8: LCD1.DB7, Onderdeel1.D11_PWM/MOSI
  N9: LCD1.LED-, Onderdeel1.GND
