# Fritzing sketch id3568_Fritzing_Schema_0 (saved by Fritzing 0.9.2b)
breadboards: 1

parts:
  Arduino = Arduino Nano (Rev3.0)
  R1 = Resistor [tolerance=±5% resistance=15k package="1206 [SMD]"]
  C1 = Electrolytic Capacitor [capacitance=100µF package="200 mil [THT, electrolytic]"]
  SCT-013-030 = Inductor [package="400 mil [THT]"]
  R2 = Resistor [tolerance=±5% resistance=15k package="1206 [SMD]"]

nets:
  N1: Arduino.GND, R1.Pin_1, C1.-
  N2: Arduino.5V, R2.Pin_1
  N3: Arduino.A1, SCT-013-030.pin_0
  N4: R1.Pin_0, C1.+, SCT-013-030.pin_1, R2.Pin_0
