# Fritzing sketch id3569_SCT013_0 (saved by Fritzing 0.9.2b)
breadboards: 1

parts:
  R1 = Resistor [tolerance=±5% resistance=10k package=THT]
  R2 = Resistor [tolerance=±5% resistance=10k package=THT]
  C1 = Electrolytic Capacitor [capacitance=10µF package="100 mil [THT, electrolytic]"]  # not connected
  Part1 = Arduino Uno (Rev3)
  MIC1 = Microphone
  R3 = Resistor [tolerance=±5% resistance=220 package="1206 [SMD]"]

nets:
  N1: R1.Pin_1, R2.Pin_0, MIC1.pin1, R3.Pin_1
  N2: R2.Pin_1, Part1.GND
  N3: Part1.A0, MIC1.pin2, R3.Pin_0
