# Fritzing sketch id356_Aprinderea_unui_LED_direct_de_la_sursa_B3JYMeL_0 (saved by Fritzing 0.9.3b)
breadboards: 1

parts:
  LED1 = smd LED [color="Red (633nm)" package="0805 [SMD]"]
  R1 = Resistor [tolerance=±5% resistance=1.6k package=THT]
  V1 = DC Power [voltage=5]

nets:
  N1: LED1.cathode, R1.Pin_0
  N2: LED1.anode, V1.V+
  GND: R1.Pin_1, V1.V-

notes:
  Vcc +5-Rosu
  GND - Albastru
  Aprinderea unui LED direct de la sursa de 5V
