# Fritzing sketch id3570_SCUNC_0 (saved by Fritzing 0.9.2b)
breadboards: 1

parts:
  IC1 = MCP3008 [part_number=MCP3008]
  U1 = RELAY [package=relay-g5q]
  Raspberry_Pi1 = Raspberry Pi 2
  Part2 = Soil Moisture Sensor 3 Pin
  M1 = DC Motor
  LED3 = LED - 3mm [color="Blue (525nm)" package="3 mm [THT]"]

nets:
  N1: IC1.connector6, Part2.connector3
  N2: IC1.connector9, IC1.connector14, Raspberry_Pi1.GND, Part2.connector2, M1.pin_2
  N3: IC1.connector10, Raspberry_Pi1.GPIO6
  N4: IC1.connector11, Raspberry_Pi1.GPIO13
  N5: IC1.connector12, Raspberry_Pi1.GPIO19
  N6: IC1.connector13, Raspberry_Pi1.GPIO26
  N7: IC1.connector15, IC1.connector16, Raspberry_Pi1.3V3, Part2.connector1
  N8: U1.COIL2, LED3.anode
  N9: U1.MAIN, M1.pin_1
  N10: U1.NC, Raspberry_Pi1.5V
  N11: U1.COIL1, Raspberry_Pi1.GPIO25, LED3.cathode

notes:
  3.3-12V Water Pump
  Analogue Sensor
  NO (normally open) Relay
  Analogue / Digital Converter (1024 bits)
