# Fritzing sketch id3572_full_0 (saved by Fritzing 0.8.7b)
breadboards: 1

parts:
  Part2 = Real Time Clock Module - DS1307 RTC Breakout Board
  SD_card_module1 = SD_Card_Module.fzp
  DHT2 = DHT11_Temperature_and_Humitidy_Sensor
  Part1 = Arduino Uno (Rev3)

nets:
  5V: Part2.5V, DHT2.connector2, Part1.5V
  GND: Part2.GND, SD_card_module1.connector7, DHT2.connector4, Part1.GND
  N1: Part2.SCL, Part1.A5/SCL
  N2: Part2.SDA, Part1.A4/SDA
  N3: SD_card_module1.connector1, Part1.3V3
  N4: SD_card_module1.connector3, Part1.D4
  N5: SD_card_module1.connector4, Part1.D10_PWM/SS
  N6: SD_card_module1.connector5, Part1.D13/SCK
  N7: SD_card_module1.connector6, Part1.D12/MISO
  N8: DHT2.connector1, Part1.D2

notes:
  RTC Module
  DHT11 Module
  SD card Module
