# Fritzing sketch id3573_BatTester_0 (saved by Fritzing 0.9.2b)
breadboards: 1

parts:
  Part1 = Arduino Uno (Rev3)
  Nokia_5110_LCD_Module4 = Nokia5110 84x48
  Nokia_5110_LCD_Module5 = Nokia5110LCDModule
  Q2 = Basic FET N-Channel [package="TO220 [THT]"]
  R4 = Resistor [tolerance=±5% resistance=10k package=THT]
  R5 = Resistor [tolerance=±5% resistance=220 package=THT]
  SPKR1 = Loudspeaker
  S1 = Pushbutton [package="[THT]"]
  R6 = Resistor [tolerance=±5% resistance=10k package=THT]
  R7 = Resistor [tolerance=±5% resistance=100 package=THT]
  VCC1 = Battery
  R8 = Resistor [tolerance=±5% resistance=100k package=THT]
  R3 = Resistor [tolerance=±2% resistance=6 package="2512 [SMD]"]
  R3_2 = Resistor [tolerance=±2% resistance=6 package="2010 [SMD]"]
  R3_3 = Resistor [tolerance=±2% resistance=6 package="2512 [SMD]"]
  R3_4 = Resistor [tolerance=±2% resistance=6 package=THT]

nets:
  N1: Part1.A0, VCC1.+, R8.Pin_1, R3.Pin_0, R3_2.Pin_0, R3_3.Pin_0, R3_4.Pin_0
  N2: Part1.A1, Q2.drain, R3.Pin_1, R3_2.Pin_1, R3_3.Pin_1, R3_4.Pin_1
  N3: Part1.D8, Nokia_5110_LCD_Module4.connector3, Nokia_5110_LCD_Module5.connector0
  N4: Part1.D9_PWM, Nokia_5110_LCD_Module4.connector2, Nokia_5110_LCD_Module5.connector1
  N5: Part1.D10_PWM/SS, Nokia_5110_LCD_Module4.connector4, Nokia_5110_LCD_Module5.connector2
  N6: Part1.D11_PWM/MOSI, Nokia_5110_LCD_Module4.connector5, Nokia_5110_LCD_Module5.connector3
  N7: Part1.D12/MISO, Nokia_5110_LCD_Module4.connector6, Nokia_5110_LCD_Module5.connector4
  N8: Part1.D5_PWM, R7.Pin_1
  N9: Part1.D6_PWM, S1.Pin_1, S1.Pin_2, R6.Pin_0
  N10: Part1.D7, Q2.gate, R4.Pin_1
  N11: Part1.3V3, Nokia_5110_LCD_Module4.connector0, Nokia_5110_LCD_Module5.connector5
  N12: Part1.5V, S1.Pin_3, S1.Pin_4
  N13: Part1.GND, Nokia_5110_LCD_Module4.connector1, Nokia_5110_LCD_Module5.connector7, Q2.source, R4.Pin_0, R5.Pin_1, SPKR1.pin1, R6.Pin_1, VCC1.-, R8.Pin_0
  N14: Nokia_5110_LCD_Module4.connector7, Nokia_5110_LCD_Module5.connector6, R5.Pin_0
  N15: SPKR1.pin2, R7.Pin_0
