# Fritzing sketch id3574_RS232TTL_0 (saved by Fritzing 0.7.4b)
stripboards: 1

parts:
  U1 = MAX232try2
  C1 = Electrolytic Capacitor [capacitance=1µF voltage=16V package="100 mil [THT, electrolytic]"]
  C2 = Electrolytic Capacitor [capacitance=1µF voltage=16V package="100 mil [THT, electrolytic]"]
  C4 = Electrolytic Capacitor [capacitance=1µF voltage=16V package="100 mil [THT, electrolytic]"]
  J7 = female pin header, 1 pin [form="♀ (female)" part_number="VCC 5V"]
  C5 = Electrolytic Capacitor [capacitance=1µF voltage=16V package="100 mil [THT, electrolytic]"]
  J8 = female pin header, 2 pins [form="♀ (female)" part_number="RS232 (1)"]
  J9 = female pin header, 2 pins [form="♀ (female)" part_number="RS232 (2)"]
  J10 = female pin header, 2 pins [form="♀ (female)" part_number="TTL (1)"]
  J11 = female pin header, 2 pins [form="♀ (female)" part_number="TTL (2)"]
  C3 = Electrolytic Capacitor [capacitance=1µF voltage=16V package="100 mil [THT, electrolytic]"]

nets:
  N1: U1.connector0, C4.+
  N2: U1.connector1, C5.+
  N3: U1.connector2, C4.-
  N4: U1.connector3, C1.+
  N5: U1.connector4, C1.-
  N6: U1.connector5, C2.-
  N7: U1.connector6, J9.pin2
  N8: U1.connector7, J9.pin1
  N9: U1.connector8, J11.pin2
  N10: U1.connector9, J11.pin1
  N11: U1.connector10, J10.pin2
  N12: U1.connector11, J10.pin1
  N13: U1.connector12, J8.pin2
  N14: U1.connector13, J8.pin1
  GND: U1.connector14, C2.+, C3.-
  N15: U1.connector15, J7.pin1, C5.-, C3.+

notes:
  Purple (TTL Tx (1))
  Grey (TTL Rx (1))
  Yellow (TTL Tx (2))
  Black (TTL Rx (2))
  Red (5V+)
  Blue (RS232Tx (1))
  White (RS232Rx (1))
  Orange (RS232Tx (2))
  Brown (RS232Rx (2))
  RS232 2 TTL
  5V+
  TX1
  RX1
  RX2
  TX2
  RS232
  TTL
  ----------
  -----
  Cut the tracks under the chip!!
