# Fritzing sketch id3575_Base_LIPO_0 (saved by Fritzing 0.9.2b)
circuit board: 3.15425cm x 7.50834cm
breadboards: 1

parts:
  XTAL8Mhz = Crystal [frequency="8 MHz" package=THT]
  MPU6050 = female pin header, 4 pins [form="♀ (female)"]
  U6 = atmega328 [package=dip]
  nRF2041 = prefix_NRF [form="♀ (female)"]
  Batt-Conn = Header 2 [package=molex-1x2_lock]
  MCP73831 = MCP73831 [package=sot23-5]
  X1 = USB Connectors [package=usb-microb]
  Q1 = MOSFET-NCHANNEL [package=sot323]
  C6 = Ceramic Capacitor [capacitance=10µF package="0805 [SMD, multilayer]"]
  D2 = Schottky Diode [part_number=1N5817 package="Melf DO-213 AB [SMD]"]
  C1 = Capacitor [package=0805]
  C2 = Capacitor [package=0805]
  R3 = Resistor [tolerance=±5% resistance=220 package="0805 [SMD]"]
  R1 = Resistor [tolerance=±5% resistance=220 package="0805 [SMD]"]
  R2 = Resistor [tolerance=±5% resistance=220 package="0805 [SMD]"]
  C4 = Capacitor [package=0805]
  C5 = Capacitor [package=0805]
  LED1 = LEDs [package=led-1206]
  S1 = SWITCH-MOMENTARY-2 [package=reed_switch_pth]
  IC1 = Switching step-up voltage regulator [package=sot23-5]  # not connected
  U7 = V_REG_TPS61040 [package=sot23-5]  # not connected

nets:
  N1: XTAL8Mhz.pin_0, U6.XLAT2, C1.1
  N2: XTAL8Mhz.pin_1, U6.XLAT1, C2.1
  N3: MPU6050.pin1, U6.A5
  N4: MPU6050.pin2, U6.A4
  GND: MPU6050.pin3, U6.GND, nRF2041.connector0, Batt-Conn.2, MCP73831.STAT, X1.GND, C6.0, C1.2, C2.2, R3.Pin_1, R2.Pin_1, C4.1, C5.1
  N5: MPU6050.pin4, U6.AVCC, nRF2041.connector7, C6.1
  N6: U6.D7, nRF2041.connector1
  N7: U6.D8, nRF2041.connector6
  N8: U6.D11_(PWM), nRF2041.connector2
  N9: U6.D12, nRF2041.connector4
  N10: U6.D13, nRF2041.connector5
  N11: Batt-Conn.1, MCP73831.VBAT, Q1.G, C5.2
  N12: MCP73831.VSS, R2.Pin_0
  N13: MCP73831.VIN, X1.VBUS, Q1.D, D2.anode, R3.Pin_0, R1.Pin_0, C4.2
  N14: MCP73831.PROG, LED1.C
  N15: Q1.S, S1.1
  N16: R1.Pin_1, LED1.A
