# Fritzing sketch id3576_Secret_Knock_Detecting_Door_Lock_0 (saved by Fritzing 0.9.0b)
breadboards: 1

parts:
  Part1 = Arduino Uno (Rev3)
  J1 = Piezo Speaker
  S1 = Pushbutton [package="[THT]"]
  D1 = Rectifier Diode [part_number=1N4001 package="300 mil [THT]"]
  M1 = DC Motor
  Q1 = NPN-Transistor [part_number=P2N2222A package="TO92 [THT]"]
  R1 = Resistor [tolerance=±5% resistance=10k package=THT]
  LED1 = LED - 5mm [color="Red (633nm)" package="5 mm [THT]"]
  LED2 = LED - 5mm [color="Green (560nm)" package="5 mm [THT]"]
  R2 = Resistor [tolerance=±5% resistance=220 package=THT]
  R3 = Resistor [tolerance=±5% resistance=220 package=THT]
  R4 = Resistor [tolerance=±5% resistance=2.2k package=THT]
  R5 = Resistor [tolerance=±5% resistance=1M package=THT]

nets:
  N1: Part1.A0, J1.pin2, R5.Pin_1
  N2: Part1.D2, S1.Pin_3, S1.Pin_4, R1.Pin_0
  N3: Part1.D3_PWM, R4.Pin_1
  N4: Part1.D4, R2.Pin_1
  N5: Part1.D5_PWM, R3.Pin_1
  N6: Part1.GND, J1.pin1, R5.Pin_0
  N7: S1.Pin_1, S1.Pin_2, D1.cathode, M1.pin_2
  N8: D1.anode, M1.pin_1, Q1.E
  N9: Q1.B, R4.Pin_0
  N10: Q1.C, R1.Pin_1, LED1.cathode, LED2.cathode
  N11: LED1.anode, R2.Pin_0
  N12: LED2.anode, R3.Pin_0
