# Fritzing sketch id3588_secuencia_led_1_0 (saved by Fritzing 0.7.5b)
breadboards: 1

parts:
  Arduino1 = Arduino
  R1 = Resistor [tolerance=±5% resistance=220 package=THT]
  R2 = Resistor [tolerance=±5% resistance=220 package=THT]
  R3 = Resistor [tolerance=±5% resistance=220 package=THT]
  R5 = Resistor [tolerance=±5% resistance=220 package=THT]
  R6 = Resistor [tolerance=±5% resistance=220 package=THT]
  R7 = Resistor [tolerance=±5% resistance=220 package=THT]
  LED1 = LED - 5mm [color="Red (633nm)" package="5 mm [THT]"]
  LED2 = LED - 5mm [color="Red (633nm)" package="5 mm [THT]"]
  LED3 = LED - 5mm [color="Red (633nm)" package="5 mm [THT]"]
  LED4 = LED - 5mm [color="Red (633nm)" package="5 mm [THT]"]
  LED5 = LED - 5mm [color="Red (633nm)" package="5 mm [THT]"]
  LED6 = LED - 5mm [color="Red (633nm)" package="5 mm [THT]"]

nets:
  N1: Arduino1.D10, LED6.anode
  N2: Arduino1.D9, LED5.anode
  N3: Arduino1.D7, LED4.anode
  N4: Arduino1.D6, LED2.anode
  N5: Arduino1.D5, LED3.anode
  N6: Arduino1.D4, LED1.anode
  N7: R1.Pin_0, R2.Pin_0, R3.Pin_0, R5.Pin_0, R6.Pin_0, R7.Pin_0
  N8: R1.Pin_1, LED1.cathode
  N9: R2.Pin_1, LED3.cathode
  N10: R3.Pin_1, LED2.cathode
  N11: R5.Pin_1, LED5.cathode
  N12: R6.Pin_1, LED4.cathode
  N13: R7.Pin_1, LED6.cathode
