# Fritzing sketch id3595_Prender_secuencia_de_Leds__por_colores_aW7QwUL_0 (saved by Fritzing 0.9.3b)
breadboards: 1

parts:
  Parte1 = Arduino Uno (Rev3)
  R1 = Resistor [tolerance=±5% resistance=220 package=THT]
  LED1 = LED - 5mm [color="Red (633nm)" package="5 mm [THT]"]
  R2 = Resistor [tolerance=±5% resistance=220 package=THT]
  R3 = Resistor [tolerance=±5% resistance=220 package=THT]
  LED4 = LED - 5mm [color="Red (633nm)" package="5 mm [THT]"]
  R4 = Resistor [tolerance=±5% resistance=220 package=THT]
  LED5 = smd LED [color="Yellow (585nm)" package="1206 [SMD]"]
  LED11 = smd LED [color="Green (555nm)" package="1206 [SMD]"]
  R5 = Resistor [tolerance=±5% resistance=220 package=THT]
  R6 = Resistor [tolerance=±5% resistance=220 package=THT]
  LED12 = smd LED [color="Yellow (585nm)" package="1206 [SMD]"]
  LED13 = smd LED [color="Green (555nm)" package="1206 [SMD]"]

nets:
  N1: Parte1.D8, LED4.anode
  N2: Parte1.D10_PWM/SS, LED12.anode
  N3: Parte1.D2, LED1.anode
  N4: Parte1.D4, LED5.anode
  N5: Parte1.D6_PWM, LED11.anode
  N6: R1.Pin_0, LED1.cathode
  N7: R2.Pin_0, LED5.cathode
  N8: R2.Pin_1, R3.Pin_1, R4.Pin_1, R5.Pin_1, R6.Pin_1
  N9: R3.Pin_0, LED11.cathode
  N10: LED4.cathode, R4.Pin_0
  N11: R5.Pin_0, LED12.cathode
  N12: R6.Pin_0, LED13.cathode
