# Fritzing sketch id3597_secuencia_de_leds_0 (saved by Fritzing 0.9.2b)
breadboards: 1

parts:
  Parte2 = Arduino Uno (Rev3)
  R7 = Resistor [tolerance=±5% resistance=220 package=THT]
  R8 = Resistor [tolerance=±5% resistance=220 package=THT]
  R9 = Resistor [tolerance=±5% resistance=220 package=THT]
  R10 = Resistor [tolerance=±5% resistance=220 package=THT]
  R11 = Resistor [tolerance=±5% resistance=220 package=THT]
  R12 = Resistor [tolerance=±5% resistance=220 package=THT]
  LED14 = LED - 5mm [color="Red (633nm)" package="5 mm [THT]"]
  LED15 = LED - 5mm [color="Red (633nm)" package="5 mm [THT]"]
  LED16 = smd LED [color="Yellow (585nm)" package="1206 [SMD]"]
  LED17 = smd LED [color="Yellow (585nm)" package="1206 [SMD]"]
  LED18 = smd LED [color="Green (555nm)" package="1206 [SMD]"]
  LED19 = smd LED [color="Green (555nm)" package="1206 [SMD]"]

nets:
  N1: Parte2.D8, LED16.anode
  N2: Parte2.D4, LED15.anode
  N3: Parte2.D5_PWM, LED17.anode
  N4: Parte2.D6_PWM, LED19.anode
  N5: Parte2.D7, LED14.anode
  N6: R7.Pin_0, LED18.cathode
  N7: R7.Pin_1, R8.Pin_1, R9.Pin_1, R10.Pin_1, R11.Pin_1, R12.Pin_1
  N8: R8.Pin_0, LED16.cathode
  N9: R9.Pin_0, LED14.cathode
  N10: R10.Pin_0, LED19.cathode
  N11: R11.Pin_0, LED17.cathode
  N12: R12.Pin_0, LED15.cathode
