# Fritzing sketch id3598_Random_8_led_flasher (saved by Fritzing 0.3.14b)
breadboards: 2

parts:
  Arduino1 = Arduino
  LED1 = Red LED - 5mm
  LED2 = Red LED - 5mm
  LED3 = Red LED - 5mm
  R1 = Resistor [resistance=220 package=THT]
  R2 = Resistor [resistance=220 package=THT]
  R3 = Resistor [resistance=220 package=THT]
  R4 = Resistor [resistance=220 package=THT]
  R5 = Resistor [resistance=220 package=THT]
  R6 = Resistor [resistance=220 package=THT]
  R7 = Resistor [resistance=220 package=THT]
  R8 = Resistor [resistance=220 package=THT]
  LED4 = Red LED - 5mm
  LED5 = Red LED - 5mm
  LED6 = Red LED - 5mm
  LED7 = Red LED - 5mm
  LED8 = Red LED - 5mm
  IC1 = DIP - 16 pins

nets:
  N1: Arduino1.D11, IC1.connector0
  N2: LED1.cathode, R3.Pin_0
  N3: LED1.anode, IC1.connector9
  N4: LED2.cathode, R7.Pin_0
  N5: LED2.anode, IC1.connector10
  N6: LED3.cathode, R8.Pin_0
  N7: LED3.anode, IC1.connector8
  N8: R1.Pin_0, LED8.cathode
  N9: R1.Pin_1, R2.Pin_1, R3.Pin_1, R4.Pin_1, R5.Pin_1, R6.Pin_1, R7.Pin_1, R8.Pin_1
  N10: R2.Pin_0, LED6.cathode
  N11: R4.Pin_0, LED7.cathode
  N12: R5.Pin_0, LED4.cathode
  N13: R6.Pin_0, LED5.cathode
  N14: LED4.anode, IC1.connector12
  N15: LED5.anode, IC1.connector11
  N16: LED6.anode, IC1.connector6
  N17: LED7.anode, IC1.connector4
  N18: LED8.anode, IC1.connector5
  N19: IC1.connector1, IC1.connector7, IC1.connector14
  N20: IC1.connector2, IC1.connector15
