# Fritzing sketch id35_MyLVD_0 (saved by Fritzing 0.9.3b)
circuit board: 8.46667cm x 5.64444cm
breadboards: 1

parts:
  Part1 = adafruit [part_number="Adafruit #2000"]
  R2 = Resistor [tolerance=±5% resistance=10k package=THT]
  12v_INPUT = Screw terminal - 2 pins [package=THT]
  OUTPUT = Screw terminal - 2 pins [package=THT]
  Q1 = MOSFET-NCHANNEL [part_number=P36NF06 package=to220v]
  R3 = Resistor [tolerance=±5% resistance=47k package=THT]

nets:
  N1: Part1.connector71, 12v_INPUT.pin2, OUTPUT.pin2, R3.Pin_1
  N2: Part1.connector72, R2.Pin_0, 12v_INPUT.pin1, Q1.S
  N3: Part1.connector76, Q1.G
  N4: Part1.connector91, R2.Pin_1, R3.Pin_0
  N5: OUTPUT.pin1, Q1.D
