# Fritzing sketch id3600_SecuenciaDeLuces_0 (saved by Fritzing 0.9.3b)
breadboards: 1

parts:
  Componente1 = Arduino Uno (Rev3)
  LED1 = LED - 5mm [color="Red (633nm)" package="5 mm [THT]"]
  LED2 = LED - 5mm [color="Red (633nm)" package="5 mm [THT]"]
  R1 = Resistor [tolerance=±5% resistance=220 package=THT]
  R2 = Resistor [tolerance=±5% resistance=220 package=THT]
  R3 = Resistor [tolerance=±5% resistance=220 package=THT]
  R4 = Resistor [tolerance=±5% resistance=220 package=THT]
  R5 = Resistor [tolerance=±5% resistance=220 package=THT]
  R6 = Resistor [tolerance=±5% resistance=220 package=THT]
  LED3 = LED - 5mm [color="Green (555nm)" package="5 mm [THT]"]
  LED4 = LED - 5mm [color="Green (555nm)" package="5 mm [THT]"]
  LED5 = LED - 5mm [color="Yellow (592nm)" package="5 mm [THT]"]
  LED6 = LED - 5mm [color="Yellow (595nm)" package="5 mm [THT]"]
  S1 = Pushbutton [package="[THT]"]
  R7 = Resistor [tolerance=±5% resistance=220 package=THT]

nets:
  N1: Componente1.D11_PWM/MOSI, S1.Pin_3, S1.Pin_4, R7.Pin_1
  N2: Componente1.D2, LED6.anode
  N3: Componente1.D3_PWM, LED5.anode
  N4: Componente1.D4, LED4.anode
  N5: Componente1.D5_PWM, LED3.anode
  N6: Componente1.D6_PWM, LED2.anode
  N7: Componente1.D7, LED1.anode
  N8: Componente1.5V, S1.Pin_1, S1.Pin_2
  N9: Componente1.GND, R1.Pin_0, R2.Pin_0, R3.Pin_0, R4.Pin_0, R5.Pin_0, R6.Pin_0, R7.Pin_0
  N10: LED1.cathode, R1.Pin_1
  N11: LED2.cathode, R2.Pin_1
  N12: R3.Pin_1, LED3.cathode
  N13: R4.Pin_1, LED4.cathode
  N14: R5.Pin_1, LED5.cathode
  N15: R6.Pin_1, LED6.cathode
