# Fritzing sketch id3604_secuencia_3_leds_0 (saved by Fritzing 0.9.3b)
breadboards: 1

parts:
  Parte1 = Arduino Uno (Rev3)
  R1 = Resistor [tolerance=±5% resistance=220 package=THT]
  LED1 = LED - 5mm [color="Red (633nm)" package="5 mm [THT]"]
  R2 = Resistor [tolerance=±5% resistance=220 package=THT]
  R3 = Resistor [tolerance=±5% resistance=220 package=THT]
  LED5 = smd LED [color="Yellow (585nm)" package="1206 [SMD]"]
  LED11 = smd LED [color="Green (555nm)" package="1206 [SMD]"]

nets:
  N1: Parte1.D4, LED1.anode
  N2: Parte1.D5_PWM, LED5.anode
  N3: Parte1.D6_PWM, LED11.anode
  N4: R1.Pin_0, LED1.cathode
  N5: R1.Pin_1, R2.Pin_1, R3.Pin_1
  N6: R2.Pin_0, LED5.cathode
  N7: R3.Pin_0, LED11.cathode
