# Fritzing sketch id360_Aquariumsteuerung1_0 (saved by Fritzing 0.9.3b)
circuit board: 10.8cm x 5.4cm
breadboards: 1

parts:
  R1 = Resistor [tolerance=±5% resistance=4.7k package=THT]
  Bauteil1 = Arduino Uno (Rev3)
  H1_128x96 = Grove OLED 128x96
  S1 = Pushbutton [package="[THT]"]
  S2 = Pushbutton [package="[THT]"]
  S3 = Pushbutton [package="[THT]"]
  S4 = Pushbutton [package="[THT]"]
  S5 = Pushbutton [package="[THT]"]
  S6 = Pushbutton [package="[THT]"]
  Q1_BUX_11 = Basic FET N-Channel [package="TO220 [THT]"]
  JP1 = Header 4 [package=molex-1x4_lock]
  R3 = Resistor [tolerance=±5% resistance=470k package=THT]
  RTC = Real Time Clock Module - DS1307 RTC Breakout Board
  R4 = Rotary Potentiometer (Small) [maximum_resistance=50kΩ package=THT]

nets (from the breadboard view):
  N1: R1.Pin_0, Q1_BUX_11.gate, R3.Pin_1
  N2: R1.Pin_1, Bauteil1.D11_PWM/MOSI
  N3: Bauteil1.A0, R4.wiper
  N4: Bauteil1.A5/SCL, H1_128x96.SCL, RTC.SCL
  N5: Bauteil1.D8, S4.Pin_1, S4.Pin_2
  N6: Bauteil1.D9_PWM, S3.Pin_1, S3.Pin_2
  N7: Bauteil1.D10_PWM/SS, S6.Pin_1, S6.Pin_2
  N8: Bauteil1.D12/MISO, S5.Pin_1, S5.Pin_2
  GND: Bauteil1.GND, H1_128x96.GND, S1.Pin_3, S1.Pin_4, S2.Pin_3, S2.Pin_4, S3.Pin_3, S3.Pin_4, S4.Pin_3, S4.Pin_4, S5.Pin_3, S5.Pin_4, S6.Pin_3, S6.Pin_4, Q1_BUX_11.source, JP1.4, R3.Pin_0, RTC.GND, R4.leg2
  N9: Bauteil1.D6_PWM, S1.Pin_1, S1.Pin_2
  N10: Bauteil1.D7, S2.Pin_1, S2.Pin_2
  5V: Bauteil1.5V, H1_128x96.VCC, RTC.5V, R4.leg1
  N11: H1_128x96.SDA, RTC.SDA
  N12: Q1_BUX_11.drain, JP1.1
  N13: JP1.2, JP1.3

notes:
  Poti 50 KOhm
