# Fritzing sketch id3610_secuencia_10_leds_Carlos_0 (saved by Fritzing 0.9.2b)
breadboards: 1

parts:
  Parte1 = Arduino Uno (Rev3)
  R1 = Resistor [tolerance=±5% resistance=220 package=THT]
  LED1 = LED - 5mm [color="Red (633nm)" package="5 mm [THT]"]
  R2 = Resistor [tolerance=±5% resistance=220 package=THT]
  R3 = Resistor [tolerance=±5% resistance=220 package=THT]
  LED4 = LED - 5mm [color="Red (633nm)" package="5 mm [THT]"]
  R4 = Resistor [tolerance=±5% resistance=220 package=THT]
  LED5 = smd LED [color="Yellow (585nm)" package="1206 [SMD]"]
  LED11 = smd LED [color="Green (555nm)" package="1206 [SMD]"]
  R5 = Resistor [tolerance=±5% resistance=220 package=THT]
  R6 = Resistor [tolerance=±5% resistance=220 package=THT]
  LED12 = smd LED [color="Yellow (585nm)" package="1206 [SMD]"]
  LED13 = smd LED [color="Green (555nm)" package="1206 [SMD]"]
  R7 = Resistor [tolerance=±5% resistance=220 package=THT]
  R8 = Resistor [tolerance=±5% resistance=220 package=THT]
  R9 = Resistor [tolerance=±5% resistance=220 package=THT]
  LED14 = LED - 5mm [color="Red (633nm)" package="5 mm [THT]"]
  LED15 = smd LED [color="Yellow (585nm)" package="1206 [SMD]"]
  R10 = Resistor [tolerance=±5% resistance=220 package=THT]
  LED16 = smd LED [color="Green (555nm)" package="1206 [SMD]"]
  LED17 = LED - 5mm [color="Red (633nm)" package="5 mm [THT]"]

nets:
  N1: Parte1.D8, LED14.anode
  N2: Parte1.D9_PWM, LED15.anode
  N3: Parte1.D10_PWM/SS, LED16.anode
  N4: Parte1.D11_PWM/MOSI, LED17.anode
  N5: Parte1.D2, LED1.anode
  N6: Parte1.D3_PWM, LED5.anode
  N7: Parte1.D4, LED11.anode
  N8: Parte1.D5_PWM, LED4.anode
  N9: Parte1.D6_PWM, LED12.anode
  N10: Parte1.D7, LED13.anode
  N11: R1.Pin_0, LED1.cathode
  N12: R1.Pin_1, R2.Pin_1, R3.Pin_1, R4.Pin_1, R5.Pin_1, R6.Pin_1, R7.Pin_0, R8.Pin_0, R9.Pin_0, R10.Pin_0
  N13: R2.Pin_0, LED5.cathode
  N14: R3.Pin_0, LED11.cathode
  N15: LED4.cathode, R4.Pin_0
  N16: R5.Pin_0, LED12.cathode
  N17: R6.Pin_0, LED13.cathode
  N18: R7.Pin_1, LED14.cathode
  N19: R8.Pin_1, LED15.cathode
  N20: R9.Pin_1, LED16.cathode
  N21: R10.Pin_1, LED17.cathode

notes:
  Proyecto elaborado por el alumno
  Carlos achulli Solar
