# Fritzing sketch id3611_SecuenciaLeds_0 (saved by Fritzing 0.7.0b)
breadboards: 1

parts:
  Arduino1 = Arduino
  LED1 = LED - 5mm [color="Red (633nm)" package="5 mm [THT]"]
  LED2 = LED - 5mm [color="Red (633nm)" package="5 mm [THT]"]
  LED3 = LED - 5mm [color="Red (633nm)" package="5 mm [THT]"]
  LED4 = LED - 5mm [color="Red (633nm)" package="5 mm [THT]"]
  LED5 = LED - 5mm [color="Red (633nm)" package="5 mm [THT]"]
  LED6 = LED - 5mm [color="Red (633nm)" package="5 mm [THT]"]
  LED7 = LED - 5mm [color="Red (633nm)" package="5 mm [THT]"]
  LED8 = LED - 5mm [color="Red (633nm)" package="5 mm [THT]"]
  R = Resistor [tolerance=±5% resistance=220 package=THT]
  R2 = Resistor [tolerance=±5% resistance=220 package=THT]
  R3 = Resistor [tolerance=±5% resistance=220 package=THT]
  R4 = Resistor [tolerance=±5% resistance=220 package=THT]
  R5 = Resistor [tolerance=±5% resistance=220 package=THT]
  R6 = Resistor [tolerance=±5% resistance=220 package=THT]
  R7 = Resistor [tolerance=±5% resistance=220 package=THT]
  R8 = Resistor [tolerance=±5% resistance=220 package=THT]
  S1 = Pushbutton [package="[THT]"]
  R_2 = Resistor [tolerance=±5% resistance=1k package=THT]

nets:
  N1: Arduino1.GND, R.Pin_0, R2.Pin_0, R3.Pin_0, R4.Pin_0, R5.Pin_0, R6.Pin_0, R7.Pin_0, R8.Pin_0, R_2.Pin_1
  N2: Arduino1.D9, LED8.anode
  N3: Arduino1.D8, LED7.anode
  N4: Arduino1.D7, LED6.anode
  N5: Arduino1.D6, LED5.anode
  N6: Arduino1.D5, LED4.anode
  N7: Arduino1.D4, LED3.anode
  N8: Arduino1.D3, LED2.anode
  N9: Arduino1.D2, LED1.anode
  N10: Arduino1.+5V, S1.Pin_1, S1.Pin_2
  N11: Arduino1.A0, S1.Pin_3, S1.Pin_4, R_2.Pin_0
  N12: LED1.cathode, R.Pin_1
  N13: LED2.cathode, R2.Pin_1
  N14: LED3.cathode, R3.Pin_1
  N15: LED4.cathode, R4.Pin_1
  N16: LED5.cathode, R5.Pin_1
  N17: LED6.cathode, R6.Pin_1
  N18: LED7.cathode, R7.Pin_1
  N19: LED8.cathode, R8.Pin_1
