# Fritzing sketch id3612_Veamos_secuencia_leds_0 (saved by Fritzing 0.9.2b)
breadboards: 1

parts:
  Componente1 = Arduino Uno (Rev3)
  R5 = Resistor [tolerance=±5% resistance=220 package=THT]
  LED8 = LED - 5mm [color="White (8000K)" package="5 mm [THT]"]
  R8 = Resistor [tolerance=±5% resistance=220 package=THT]
  R9 = Resistor [tolerance=±5% resistance=220 package=THT]
  R10 = Resistor [tolerance=±5% resistance=220 package=THT]
  R11 = Resistor [tolerance=±5% resistance=220 package=THT]
  R12 = Resistor [tolerance=±5% resistance=220 package=THT]
  LED9 = LED - 5mm [color="White (8000K)" package="5 mm [THT]"]
  LED10 = LED - 5mm [color="White (8000K)" package="5 mm [THT]"]
  LED11 = LED - 5mm [color="White (8000K)" package="5 mm [THT]"]
  LED12 = LED - 5mm [color="White (8000K)" package="5 mm [THT]"]
  S1 = Pushbutton [package="[THT]"]

nets:
  N1: Componente1.A0, R5.Pin_1, S1.Pin_3, S1.Pin_4
  N2: Componente1.D9_PWM, LED9.anode
  N3: Componente1.D10_PWM/SS, LED8.anode
  N4: Componente1.D3_PWM, LED12.anode
  N5: Componente1.D5_PWM, LED11.anode
  N6: Componente1.D6_PWM, LED10.anode
  N7: Componente1.5V, S1.Pin_1, S1.Pin_2
  N8: Componente1.GND, R5.Pin_0, R8.Pin_0, R9.Pin_0, R10.Pin_0, R11.Pin_0, R12.Pin_0
  N9: LED8.cathode, R8.Pin_1
  N10: R9.Pin_1, LED9.cathode
  N11: R11.Pin_1, LED11.cathode
  N12: R12.Pin_1, LED12.cathode
