# Fritzing sketch id3613_Secuencia_proyecto_0 (saved by Fritzing 0.9.3b)
breadboards: 1

parts:
  Parte1 = Arduino Uno (Rev3)
  R1 = Resistor [tolerance=±5% resistance=220 package=THT]
  LED1 = LED - 5mm [color="Red (633nm)" package="5 mm [THT]"]
  R2 = Resistor [tolerance=±5% resistance=220 package=THT]
  R3 = Resistor [tolerance=±5% resistance=220 package=THT]
  LED5 = smd LED [color="Yellow (585nm)" package="1206 [SMD]"]
  LED11 = smd LED [color="Green (555nm)" package="1206 [SMD]"]
  LED12 = LED - 5mm [color="Red (633nm)" package="5 mm [THT]"]
  LED13 = smd LED [color="Yellow (585nm)" package="1206 [SMD]"]
  LED14 = smd LED [color="Green (555nm)" package="1206 [SMD]"]
  R4 = Resistor [tolerance=±5% resistance=220 package=THT]
  R5 = Resistor [tolerance=±5% resistance=220 package=THT]
  R6 = Resistor [tolerance=±5% resistance=220 package=THT]

nets:
  N1: Parte1.D8, LED13.anode
  N2: Parte1.D9_PWM, LED14.anode
  N3: Parte1.D4, LED11.anode
  N4: Parte1.D5_PWM, LED5.anode
  N5: Parte1.D6_PWM, LED1.anode
  N6: Parte1.D7, LED12.anode
  N7: Parte1.GND, R1.Pin_1, R2.Pin_1, R3.Pin_1, R4.Pin_1, R5.Pin_1, R6.Pin_1
  N8: R1.Pin_0, LED11.cathode
  N9: LED1.cathode, R3.Pin_0
  N10: R2.Pin_0, LED5.cathode
  N11: LED12.cathode, R4.Pin_0
  N12: LED13.cathode, R5.Pin_0
  N13: LED14.cathode, R6.Pin_0
