# Fritzing sketch id3614_rfid_with_servo_0 (saved by Fritzing 0.9.3b)
breadboards: 3

parts:
  Arduino_UNO = Arduino Uno (Rev3)
  LCD_1602 = LCD screen
  VCC = Battery [part_number=18650]  # not connected
  R1 = Rotary Potentiometer (Small) [maximum_resistance=100kΩ package=THT]
  C1 = Electrolytic Capacitor [capacitance=1µF package="100 mil [THT, electrolytic]"]
  J1 = Basic Servo
  LED1 = LED - 5mm [color="Green (570nm)" package="5 mm [THT]"]
  R2 = Resistor [tolerance=±5% resistance=220 package=THT]
  LED2 = LED - 5mm [color="Red (633nm)" package="5 mm [THT]"]
  R3 = Resistor [tolerance=±5% resistance=220 package=THT]
  J2 = Piezo Speaker

nets:
  N1: Arduino_UNO.D8, J2.pin2
  N2: Arduino_UNO.D9_PWM, J1.pulse
  N3: Arduino_UNO.D10_PWM/SS, LED1.anode
  N4: Arduino_UNO.D11_PWM/MOSI, LCD_1602.E
  N5: Arduino_UNO.D12/MISO, LCD_1602.RS
  N6: Arduino_UNO.D13/SCK, LED2.anode
  GND: Arduino_UNO.GND, LCD_1602.VSS, LCD_1602.R/W, LCD_1602.LED-, R1.leg1, C1.+, J1.gnd, R2.Pin_1, R3.Pin_1, J2.pin1
  N7: Arduino_UNO.D4, LCD_1602.DB7
  N8: Arduino_UNO.D5_PWM, LCD_1602.DB6
  N9: Arduino_UNO.D6_PWM, LCD_1602.DB5
  N10: Arduino_UNO.D7, LCD_1602.DB4
  5V: Arduino_UNO.5V, LCD_1602.VDD, LCD_1602.LED+, R1.leg2, C1.-, J1.vcc
  N11: LCD_1602.V0, R1.wiper
  N12: LED1.cathode, R2.Pin_0
  N13: LED2.cathode, R3.Pin_0

notes:
  Vin = 7.4 Volts
  RDM6300
  Rx VCC
  Tx GND
  ANT + -
  ANT
  Tag
  Card
