# Fritzing sketch id3615_SecurityBox_0 (saved by Fritzing 0.7.10b)
breadboards: 1

parts:
  Arduino1 = Arduino
  R1 = Resistor [tolerance=±5% resistance=220 package=THT]
  S1 = Pushbutton [package="[THT]"]
  S2 = Pushbutton [package="[THT]"]
  R2 = Resistor [tolerance=±5% resistance=220 package=THT]
  S3 = Pushbutton [package="[THT]"]
  S4 = Pushbutton [package="[THT]"]
  R3 = Resistor [tolerance=±5% resistance=220 package=THT]
  R4 = Resistor [tolerance=±5% resistance=220 package=THT]

nets:
  N1: Arduino1.D12, Arduino1.D11, Arduino1.D10, Arduino1.D9, Arduino1.+5V, S1.Pin_1, S1.Pin_2, S2.Pin_1, S2.Pin_2, S3.Pin_1, S3.Pin_2, S4.Pin_1, S4.Pin_2
  N2: Arduino1.GND, R1.Pin_1, R2.Pin_1, R3.Pin_1, R4.Pin_1
  N3: R1.Pin_0, S1.Pin_3, S1.Pin_4
  N4: S2.Pin_3, S2.Pin_4, R2.Pin_0
  N5: S3.Pin_3, S3.Pin_4, R3.Pin_0
  N6: S4.Pin_3, S4.Pin_4, R4.Pin_0
