# Fritzing sketch id3617_culm_0 (saved by Fritzing 0.9.1b)
breadboards: 2

parts:
  Part1 = Arduino Uno (Rev3) - ICSP
  S1 = Momentary Switch [package=ksa_sealed_tac_switch]
  R1 = Resistor [package="2512 [SMD]"]
  S2 = Momentary Switch [package=ksa_sealed_tac_switch]
  R2 = Resistor [package="2512 [SMD]"]
  S3 = Momentary Switch [package=ksa_sealed_tac_switch]
  R3 = Resistor [package="2512 [SMD]"]
  S4 = Momentary Switch [package=ksa_sealed_tac_switch]
  R4 = Resistor [package="2512 [SMD]"]
  S5 = Momentary Switch [package=ksa_sealed_tac_switch]
  R5 = Resistor [package="2512 [SMD]"]
  LED1 = smd LED [color="Red (633nm)" package="1206 [SMD]"]
  R6 = Resistor [package="2512 [SMD]"]
  J1 = Piezo Speaker
  IC1 = L293D [package=THT]
  VCC1 = Battery block 9V
  S6 = Momentary Switch [package=ksa_sealed_tac_switch]
  S7 = Momentary Switch [package=ksa_sealed_tac_switch]
  S8 = Momentary Switch [package=ksa_sealed_tac_switch]
  R7 = Resistor [package="2512 [SMD]"]
  R8 = Resistor [package="2512 [SMD]"]
  R9 = Resistor [package="2512 [SMD]"]
  R10 = Resistor [package="2512 [SMD]"]
  LED2 = smd LED [color="Red (633nm)" package="1206 [SMD]"]

nets:
  N1: Part1.A0, Part1.GND, R1.Pin_1, R2.Pin_1, R3.Pin_1, R4.Pin_1, R5.Pin_1, R6.Pin_1, J1.pin1, IC1.0V, IC1.Enable_2, VCC1.-, R7.Pin_0, R8.Pin_0, R9.Pin_0, R10.Pin_1
  N2: Part1.A1, S7.1, R8.Pin_1
  N3: Part1.A2, S8.1, R9.Pin_1
  N4: Part1.ICSP_MISO, Part1.D12/MISO, S1.4, R1.Pin_0
  N5: Part1.ICSP_MOSI, Part1.D11_PWM/MOSI, S2.4, R2.Pin_0
  N6: Part1.D8, S5.4, R5.Pin_0
  N7: Part1.D9_PWM, S4.4, R4.Pin_0
  N8: Part1.D10_PWM/SS, S3.4, R3.Pin_0
  N9: Part1.D13/SCK, IC1.In_4
  N10: Part1.D2, IC1.In_3
  N11: Part1.D3_PWM, S6.1, R7.Pin_1
  N12: Part1.D4, LED2.cathode
  N13: Part1.D7, LED1.cathode
  N14: Part1.5V, S1.2, S2.2, S3.2, S4.2, S5.2, J1.pin2, IC1.Out_3_(_Controlled_by_Enable_2_), IC1.Out_4_(_Controlled_by_Enable_2_), IC1.+V, VCC1.+, S6.3, S7.3, S8.3
  N15: LED1.anode, R6.Pin_0
  N16: R10.Pin_0, LED2.anode

notes:
  motor button to close door, arm mode active, arm mode deactive
  Input button 0, 1, 2, 3, start this led should be green
  Ultrasonic Sensor should go here
