# Fritzing sketch id3618_Untitled_Sketch_2_0 (saved by Fritzing 0.9.3b)
breadboards: 1

parts:
  Part1 = Arduino Pro
  R1 = Resistor [tolerance=±5% resistance=220 package="0603 [SMD]"]
  R2 = Resistor [tolerance=±5% resistance=220 package="0603 [SMD]"]
  R3 = Resistor [tolerance=±5% resistance=220 package="0603 [SMD]"]
  R4 = Resistor [tolerance=±5% resistance=220 package="0603 [SMD]"]
  R5 = Resistor [tolerance=±5% resistance=220 package="0603 [SMD]"]
  R6 = Resistor [tolerance=±5% resistance=220 package="0603 [SMD]"]
  R7 = Resistor [tolerance=±5% resistance=220 package="0603 [SMD]"]
  R8 = Resistor [tolerance=±5% resistance=220 package="0603 [SMD]"]
  U1 = 7-SEGMENT-DISPLAY [package=7-segment-display]
  HEF1 = HEF4094 [package="DIP16 [THT]"]

nets:
  N1: Part1.D8, HEF1.Q7
  N2: Part1.D11/MOSI, HEF1.Q5
  N3: Part1.D12/MISO, HEF1.Q8
  3V3: Part1.3V3, HEF1.Q's, HEF1.Vdd
  GND: Part1.GND, U1.C, U1.F, HEF1.Vss, HEF1.Q6
  N4: R1.Pin_0, U1.E
  N5: R1.Pin_1, HEF1.Q4
  N6: R2.Pin_0, U1.G
  N7: R2.Pin_1, HEF1.DATA
  N8: R3.Pin_0, U1.G2
  N9: R3.Pin_1, HEF1.CLOCK
  N10: R4.Pin_0, U1.A
  N11: R4.Pin_1, HEF1.Q1
  N12: R5.Pin_0, HEF1.STROBE
  N13: R5.Pin_1, U1.D
  N14: R6.Pin_0, HEF1.OE
  N15: R6.Pin_1, U1.G1
  N16: R7.Pin_0, HEF1.Q2
  N17: R7.Pin_1, U1.DP
  N18: R8.Pin_0, HEF1.Q3
  N19: R8.Pin_1, U1.B
