# Fritzing sketch id3619_Arduino_wireless_segnalator_0 (saved by Fritzing 0.9.2b)
breadboards: 2

parts:
  KY-6 = keyes
  S2 = Momentary Switch [package=ksa_sealed_tac_switch]
  U12 = RF_RX
  LED2 = smd LED [color="Red (633nm)" package="1206 [SMD]"]
  R2 = Resistor [tolerance=±5% resistance=10k package="0603 [SMD]"]
  U11 = CustomPart
  S3 = Momentary Switch [package=ksa_sealed_tac_switch]
  R11 = Resistor [tolerance=±5% resistance=10k package="0603 [SMD]"]
  R12 = Trimmer Potentiometer [maximum_resistance=10kΩ package=THT]
  R6 = Resistor [tolerance=±5% resistance=10k package="0603 [SMD]"]
  LCD1 = LCD screen
  PIR2 = PIR_sensor
  R10 = Resistor [tolerance=±5% resistance=1k package="0603 [SMD]"]
  ANT2 = Antenna
  LCD2 = LCD screen
  R9 = Resistor [tolerance=±5% resistance=10k package="0603 [SMD]"]
  U9 = RF_RX
  R8 = Resistor [tolerance=±5% resistance=10k package="0603 [SMD]"]
  LED1 = smd LED [color="Red (633nm)" package="1206 [SMD]"]
  U8 = CustomPart
  U13 = SWITCH-SPST-2 [package=r_sw_th]
  R1 = Resistor [tolerance=±5% resistance=10k package="0603 [SMD]"]
  R7 = Resistor [tolerance=±5% resistance=10k package="0603 [SMD]"]
  R5 = Trimmer Potentiometer [maximum_resistance=10kΩ package=THT]
  U10 = SWITCH-SPST-2 [package=r_sw_th]
  ANT1 = Antenna
  S1 = Momentary Switch [package=ksa_sealed_tac_switch]
  PIR3 = PIR_sensor
  Componente2 = Arduino Uno (Rev3)
  KY-5 = keyes
  S4 = Momentary Switch [package=ksa_sealed_tac_switch]
  R3 = Resistor [tolerance=±5% resistance=10k package="0603 [SMD]"]
  R4 = Resistor [tolerance=±5% resistance=1k package="0603 [SMD]"]
  Componente1 = Arduino Uno (Rev3)

nets:
  N1: KY-6.connector0, Componente2.D10_PWM/SS
  VDD: KY-6.connector1, U12.connector4, U11.connector3, S3.3, R11.Pin_1, R12.leg1, LCD2.VDD, PIR3.connector1, Componente2.D12/MISO, Componente2.5V, S4.3
  VSS: KY-6.connector2, KY-6.connector4, U12.connector1, LED2.anode, U11.connector2, R12.leg2, LCD2.VSS, LCD2.R/W, R9.Pin_0, R8.Pin_0, U13.O, R7.Pin_0, PIR3.connector3, Componente2.GND
  N2: S2.1, Componente1.D11_PWM/MOSI
  N3: S2.2, R1.Pin_1
  VDD_2: S2.3, R6.Pin_1, LCD1.VDD, PIR2.connector1, U9.connector4, U8.connector3, R5.leg1, S1.3, KY-5.connector1, Componente1.D12/MISO, Componente1.5V
  N4: U12.connector3, Componente2.D0/RX
  N5: LED2.cathode, R10.Pin_1
  VSS_2: R2.Pin_0, LCD1.VSS, LCD1.R/W, PIR2.connector3, U9.connector1, LED1.anode, U8.connector2, R1.Pin_0, R5.leg2, U10.O, KY-5.connector2, KY-5.connector4, R3.Pin_0, Componente1.GND
  N6: R2.Pin_1, S1.2
  N7: U11.connector0, ANT2.antenna_lead
  N8: S3.1, Componente2.D9_PWM
  N9: S3.2, R9.Pin_1
  N10: R11.Pin_0, LCD2.LED+
  N11: R12.wiper, LCD2.V0
  N12: R6.Pin_0, LCD1.LED+
  N13: LCD1.V0, R5.wiper
  N14: LCD1.RS, Componente1.D7
  N15: LCD1.E, Componente1.D6_PWM
  N16: LCD1.DB4, Componente1.D5_PWM
  N17: LCD1.DB5, Componente1.D4
  N18: LCD1.DB6, Componente1.D3_PWM
  N19: LCD1.DB7, Componente1.D2
  N20: LCD1.LED-, U10.P
  N21: PIR2.connector2, R3.Pin_1
  N22: R10.Pin_0, Componente2.D8
  N23: LCD2.RS, Componente2.D7
  N24: LCD2.E, LCD2.DB0, Componente2.D6_PWM
  N25: LCD2.DB4, Componente2.D5_PWM
  N26: LCD2.DB5, Componente2.D4
  N27: LCD2.DB6, Componente2.D3_PWM
  N28: LCD2.DB7, Componente2.D2
  N29: LCD2.LED-, U13.P
  N30: U9.connector3, Componente1.D0/RX
  N31: R8.Pin_1, PIR3.connector2
  N32: LED1.cathode, R4.Pin_1
  N33: U8.connector0, ANT1.antenna_lead
  N34: R7.Pin_1, S4.2
  N35: S1.1, Componente1.D9_PWM
  N36: Componente2.D11_PWM/MOSI, S4.1
  N37: KY-5.connector0, Componente1.D10_PWM/SS
  N38: R4.Pin_0, Componente1.D8

notes:
  Lampada
  Pulsante assegna il numero al palo.
  Pulsante ricevi solo da palo numero X.
  PALO N 1
  PALO N 2
  Autore : Alessandro Oss
