# Fritzing sketch id3621_SEGUIDOR_DE_LINEA_0 (saved by Fritzing 0.7.4b)
breadboards: 1

parts:
  IC1 = L293D [package=THT]
  Arduino1 = Arduino
  J1 = female pin header, 2 pins [form="♀ (female)"]
  J2 = female pin header, 2 pins [form="♀ (female)"]
  J3 = Screw terminal - 2 pins [package=THT]
  J4 = Screw terminal - 2 pins [package=THT]
  J5 = female pin header, 2 pins [form="♀ (female)"]
  J6 = female pin header, 2 pins [form="♀ (female)"]
  J7 = female pin header, 2 pins [form="♀ (female)"]
  J8 = female pin header, 2 pins [form="♀ (female)"]
  J9 = female pin header, 2 pins [form="♀ (female)"]
  J10 = female pin header, 2 pins [form="♀ (female)"]

nets:
  N1: IC1.Enable_1, Arduino1.D5
  N2: IC1.In_1, Arduino1.D4
  N3: IC1.Out_1_(_Controlled_by_Enable_1_), J4.pin1
  N4: IC1.0V, Arduino1.GND, J1.pin1, J2.pin2, J5.pin1, J5.pin2, J6.pin1, J6.pin2, J7.pin1, J7.pin2
  N5: IC1.Out_2_(_Controlled_by_Enable_1_), J4.pin2
  N6: IC1.In_2, Arduino1.D3
  N7: IC1.+Vmotor, Arduino1.VIN, J1.pin2, J2.pin1
  N8: IC1.Enable_2, Arduino1.D6
  N9: IC1.In_3, Arduino1.D7
  N10: IC1.Out_3_(_Controlled_by_Enable_2_), J3.pin1
  N11: IC1.Out_4_(_Controlled_by_Enable_2_), J3.pin2
  N12: IC1.In_4, Arduino1.D8
  N13: IC1.+V, Arduino1.+5V, J8.pin1, J8.pin2, J9.pin1, J9.pin2, J10.pin1, J10.pin2
