# Fritzing sketch id3622_SEGUNDERO_0 (saved by Fritzing 0.9.3b)
breadboards: 1

parts:
  Componente1 = Arduino Uno (Rev3) - ICSP
  LED1 = 7-SEGMENT-4DIGIT-YOUNGSUN [package=7-segment-4digit-youngsun-longpads]

nets:
  N1: Componente1.D8, LED1.A
  N2: Componente1.GND, LED1.DIG3, LED1.COL-C, LED1.C, LED1.B
  N3: Componente1.D2, LED1.G
  N4: Componente1.D3_PWM, LED1.F
  N5: Componente1.D4, LED1.DIG1
  N6: Componente1.D5_PWM, LED1.E
  N7: Componente1.D6_PWM, LED1.COL-A
  N8: Componente1.D7, LED1.DIG2
