# Fritzing sketch id3623_selecteur_couleur_V3_0 (saved by Fritzing 0.9.3b)
perfboards: 1

parts:
  R3 = Resistor [tolerance=±5% resistance=220 package=THT]
  R1 = Resistor [tolerance=±5% resistance=220 package=THT]
  J11 = male pin header, 3 pins [form="♂ (male)"]
  J12 = male pin header, 3 pins [form="♂ (male)"]
  J13 = male pin header, 3 pins [form="♂ (male)"]
  J14 = male pin header, 3 pins [form="♂ (male)"]
  S1 = Toggle Switch [package=THT]
  LED1 = RGB LED - (4 legs) [package="5 mm [THT]"]
  R2 = Resistor [tolerance=±5% resistance=220 package=THT]
  R4 = Resistor [tolerance=±5% resistance=10k package=THT]
  J10 = male pin header, 3 pins [form="♂ (male)"]

nets:
  N1: R3.Pin_0, LED1.red_cathode
  N2: R3.Pin_1, J12.pin1, J14.pin1
  N3: R1.Pin_0, LED1.blue_cathode
  N4: R1.Pin_1, J12.pin3, J14.pin3
  N5: J11.pin1, J11.pin2, J11.pin3, S1.L1
  N6: J12.pin2, J14.pin2, R2.Pin_1
  N7: J13.pin1, J13.pin2, J13.pin3, S1.L2, R4.Pin_1, J10.pin1
  N8: S1.COM, J10.pin3
  N9: LED1.common_anode, R4.Pin_0, J10.pin2
  N10: LED1.green_cathode, R2.Pin_0
