# Fritzing sketch id3624_Self_Driving_Robot_0 (saved by Fritzing 0.9.1b)
breadboards: 1

parts:
  Part3 = Intel Edison Arduinobreakout
  M1 = DC Motor
  M2 = DC Motor

nets:
  N1: Part3.D10_PWM/SS, M2.pin_1
  N2: Part3.D11_PWM/MOSI, M1.pin_1
  N3: Part3.GND, M1.pin_2, M2.pin_2
