# Fritzing sketch id3626_Untitled_Sketch2_0 (saved by Fritzing 0.9.3b)
circuit board: 8.46667cm x 5.64444cm
perfboards: 1

parts:
  IC1 = L293D [package=THT]
  Onderdeel1 = Arduino Mega 2560 (Rev3)
  U2 = SPM0204UD5 [package=spm0204ud5]
  M1 = DC Motor
  J9 = female pin header, 11 pins [form="♀ (female)"]
  J8 = female pin header, 2 pins [form="♀ (female)"]
  J10 = female pin header, 2 pins [form="♀ (female)"]
  CONN1 = USB connector [package=THT]
  M2 = DC Motor

nets:
  N1: IC1.Enable_1, Onderdeel1.D13_PWM, J9.pin4
  N2: IC1.In_1, Onderdeel1.D12_PWM, J9.pin5
  N3: IC1.Out_1_(_Controlled_by_Enable_1_), J10.pin1, M2.pin_2
  GND: IC1.0V, Onderdeel1.GND, U2.GND, J9.pin1, CONN1.GND, CONN1.chassis5, CONN1.chassis6
  N4: IC1.Out_2_(_Controlled_by_Enable_1_), J10.pin2, M2.pin_1
  N5: IC1.In_2, Onderdeel1.D11_PWM, J9.pin6
  VIN: IC1.+Vmotor, Onderdeel1.VIN, U2.VS, J9.pin2, CONN1.5V
  N6: IC1.Enable_2, Onderdeel1.D10_PWM, J9.pin7
  N7: IC1.In_3, Onderdeel1.D9_PWM, J9.pin8
  N8: IC1.Out_3_(_Controlled_by_Enable_2_), M1.pin_1, J8.pin1
  N9: IC1.Out_4_(_Controlled_by_Enable_2_), M1.pin_2, J8.pin2
  N10: IC1.In_4, Onderdeel1.D8_PWM, J9.pin9
  N11: IC1.+V, Onderdeel1.5V, J9.pin3
  N12: Onderdeel1.D6_PWM, U2.GND#, J9.pin11
  N13: Onderdeel1.D7_PWM, U2.OUT, J9.pin10
