# Fritzing sketch id3628_Untitled_Sketch_0 (saved by Fritzing 0.9.2b)
breadboards: 1

parts:
  R1 = Resistor [tolerance=±5% resistance=220 package=THT]
  Componente1 = Arduino Uno (Rev3)
  R2 = Resistor [tolerance=±5% resistance=220 package=THT]
  LED2 = LED - 5mm [color="Yellow (595nm)" package="5 mm [THT]"]
  LED3 = LED - 5mm [color="Green (570nm)" package="5 mm [THT]"]
  R3 = Resistor [tolerance=±5% resistance=220 package=THT]
  LED4 = LED - 5mm [color="Red (633nm)" package="5 mm [THT]"]

nets:
  N1: R1.Pin_0, LED4.anode
  N2: R1.Pin_1, Componente1.D10_PWM/SS
  N3: Componente1.D8, R3.Pin_1
  N4: Componente1.D9_PWM, R2.Pin_1
  N5: Componente1.GND, LED2.cathode, LED3.cathode, LED4.cathode
  N6: R2.Pin_0, LED2.anode
  N7: LED3.anode, R3.Pin_0
