# Fritzing sketch id3629_PCB_Semaforo_3_led_0 (saved by Fritzing 0.9.0b)
circuit board: 10.4345cm x 6.91775cm
breadboards: 1

parts:
  LED3 = LED - 5mm [color="Red (633nm)" package="5 mm [THT]"]
  R3 = Resistor [tolerance=±5% resistance=220 package=THT]
  R5 = Resistor [tolerance=±5% resistance=10k package=THT]
  R4 = Resistor [tolerance=±5% resistance=220 package=THT]
  R2 = Resistor [tolerance=±5% resistance=220 package=THT]
  LED1 = LED - 5mm [color="Green (555nm)" package="5 mm [THT]"]
  LED4 = LED - 5mm [color="Yellow (595nm)" package="5 mm [THT]"]
  S2 = Pushbutton [package="[THT]"]
  Parte1 = Arduino Nano (Rev3.0)

nets (from the pcb view):
  N1: LED3.cathode, LED4.cathode
  N2: LED3.anode, R3.Pin_1
  N3: R3.Pin_0, Parte1.D7
  N4: R5.Pin_0, LED1.cathode, S2.Pin_1, S2.Pin_2, Parte1.GND
  N5: R5.Pin_1, Parte1.5V
  N6: R4.Pin_0, Parte1.D6
  N7: R4.Pin_1, LED4.anode
  N8: R2.Pin_0, Parte1.D5
  N9: R2.Pin_1, LED1.anode
  N10: S2.Pin_3, S2.Pin_4, Parte1.D9
