# Fritzing sketch id362_aquarium_1_0 (saved by Fritzing 0.9.0b)
circuit board: 8.46667cm x 5.64444cm
breadboards: 1

parts:
  Tiny_RTC = tinyRTC
  LCD1 = LCD screen
  R1 = Resistor [tolerance=±5% resistance=220 package=THT]
  Arduino_UNO = Arduino Uno (Rev3)
  R2 = Trimmer Potentiometer [maximum_resistance=10kΩ package=THT]
  T1 = TMP36 Temperature Sensor [package="TO92 [THT]"]
  C1 = Ceramic Capacitor [capacitance=100nF package="100 mil [THT, multilayer]"]
  S5 = Pushbutton [package="[THT]"]
  S4 = Pushbutton [package="[THT]"]
  S3 = Pushbutton [package="[THT]"]
  S2 = Pushbutton [package="[THT]"]
  S1 = Pushbutton [package="[THT]"]
  R7 = Resistor [tolerance=±5% resistance=2.2k package=THT]
  R6 = Resistor [tolerance=±5% resistance=1k package=THT]
  R5 = Resistor [tolerance=±5% resistance=680 package=THT]
  R4 = Resistor [tolerance=±5% resistance=330 package=THT]
  R3 = Resistor [tolerance=±5% resistance=2k package=THT]
  U1 = LM 358 Dual Op-Amp [package="DIP8 [THT]"]
  R8 = Resistor [tolerance=±5% resistance=220 package=THT]
  R9 = Resistor [tolerance=±5% resistance=10k package=THT]
  R10 = Resistor [tolerance=±5% resistance=500 package=THT]
  LED2 = LED - 5mm [color="Red (633nm)" package="5 mm [THT]"]
  LED3 = LED - 5mm [color="Yellow (585nm)" package="5 mm [THT]"]
  LED4 = LED - 5mm [color="Green (555nm)" package="5 mm [THT]"]
  LED5 = LED - 5mm [color="Blue (470nm)" package="5 mm [THT]"]
  R11 = Resistor [tolerance=±5% resistance=1k package=THT]
  R12 = Resistor [tolerance=±5% resistance=1k package=THT]
  R13 = Resistor [tolerance=±5% resistance=1k package=THT]
  R14 = Resistor [tolerance=±5% resistance=1k package=THT]
  LED1 = LED - 5mm [color="Green (570nm)" package="5 mm [THT]"]
  R15 = Resistor [tolerance=±5% resistance=1k package=THT]
  LDD-1000H2 = ldd-mh
  LDD-1000H1 = ldd-mh
  J1_-_18V = Power Jack [package=power_jack_smd]
  Power_LED9 = powerled
  Power_LED4 = powerled
  Power_LED1 = powerled
  Power_LED7 = powerled
  Power_LED6 = powerled
  Power_LED3 = powerled
  Power_LED5 = powerled
  Power_LED2 = powerled
  Power_LED8 = powerled

nets (from the schematic view):
  N1: Tiny_RTC.connector1, Arduino_UNO.A5/SCL
  N2: Tiny_RTC.connector2, Arduino_UNO.A4/SDA
  VDD: Tiny_RTC.connector3, LCD1.VDD, R1.Pin_0, Arduino_UNO.AREF, Arduino_UNO.5V, R2.leg2, T1.+Vs, C1.1, R3.Pin_0, U1.connector7
  GND: Tiny_RTC.connector4, LCD1.VSS, LCD1.R/W, LCD1.LED-, Arduino_UNO.GND, R2.leg1, T1.GND, C1.0, S5.Pin_1, S5.Pin_2, S4.Pin_1, S4.Pin_2, S3.Pin_1, S3.Pin_2, S2.Pin_1, S2.Pin_2, S1.Pin_1, S1.Pin_2, U1.connector3, R8.Pin_0, R9.Pin_0, R11.Pin_0, R12.Pin_0, R13.Pin_0, R14.Pin_0, R15.Pin_0
  N3: LCD1.V0, R2.wiper
  N4: LCD1.RS, Arduino_UNO.D13/SCK
  N5: LCD1.E, Arduino_UNO.D12/MISO
  N6: LCD1.DB4, Arduino_UNO.D5_PWM
  N7: LCD1.DB5, Arduino_UNO.D4
  N8: LCD1.DB6, Arduino_UNO.D3_PWM
  N9: LCD1.DB7, Arduino_UNO.D2
  N10: LCD1.LED+, R1.Pin_1
  N11: Arduino_UNO.A0, U1.connector6, R9.Pin_1, R10.Pin_0
  N12: Arduino_UNO.A1, S1.Pin_3, S1.Pin_4, R4.Pin_0, R3.Pin_1
  Switch_2: Arduino_UNO.D8, LED5.anode
  Switch_1: Arduino_UNO.D9_PWM, LED4.anode
  Light_2: Arduino_UNO.D10_PWM/SS, LED3.anode, LDD-1000H2.connector4
  Light_1: Arduino_UNO.D11_PWM/MOSI, LED2.anode, LDD-1000H1.connector4
  N13: Arduino_UNO.D7, LED1.anode
  N14: T1.Vout, U1.connector4
  N15: S5.Pin_3, S5.Pin_4, R7.Pin_1
  N16: S4.Pin_3, S4.Pin_4, R7.Pin_0, R6.Pin_1
  N17: S3.Pin_3, S3.Pin_4, R6.Pin_0, R5.Pin_1
  N18: S2.Pin_3, S2.Pin_4, R5.Pin_0, R4.Pin_1
  N19: U1.connector5, R8.Pin_1, R10.Pin_1
  N20: LED2.cathode, R11.Pin_1
  N21: LED3.cathode, R12.Pin_1
  N22: LED4.cathode, R13.Pin_1
  N23: LED5.cathode, R14.Pin_1
  N24: LED1.cathode, R15.Pin_1
  N25: LDD-1000H2.connector1, LDD-1000H1.connector1, J1_-_18V.GND
  N26: LDD-1000H2.connector2, LDD-1000H1.connector2, J1_-_18V.PWR
  N27: LDD-1000H2.connector25, Power_LED5.connector1
  N28: LDD-1000H2.connector28, Power_LED9.connector4
  N29: LDD-1000H1.connector25, Power_LED1.connector1
  N30: LDD-1000H1.connector28, Power_LED4.connector4
  N31: Power_LED9.connector1, Power_LED8.connector4
  N32: Power_LED4.connector1, Power_LED3.connector4
  N33: Power_LED1.connector4, Power_LED2.connector1
  N34: Power_LED7.connector1, Power_LED6.connector4
  N35: Power_LED7.connector4, Power_LED8.connector1
  N36: Power_LED6.connector1, Power_LED5.connector4
  N37: Power_LED3.connector1, Power_LED2.connector4

notes:
  Light_1
  Light_2
  Switch_1
  Switch_2
