# Fritzing sketch id3631_AnitaMonroed_0 (saved by Fritzing 0.9.2b)
breadboards: 1

parts:
  Parte1 = Arduino Uno (Rev3)
  J1 = Piezo Speaker
  R1 = Resistor [tolerance=±5% resistance=220 package=THT]
  R2 = Resistor [tolerance=±5% resistance=220 package=THT]
  LED1 = LED - 5mm [color="Red (633nm)" package="5 mm [THT]"]
  R3 = Resistor [tolerance=±5% resistance=220 package=THT]
  LED4 = LED - 5mm [color="Red (633nm)" package="5 mm [THT]"]
  LED5 = LED - 5mm [color="Red (633nm)" package="5 mm [THT]"]

nets:
  N1: Parte1.GND, J1.pin1, R1.Pin_0, R2.Pin_0, R3.Pin_0
  N2: Parte1.D2, LED4.cathode
  N3: Parte1.D4, LED5.cathode
  N4: Parte1.D6_PWM, J1.pin2, LED1.cathode
  N5: R1.Pin_1, LED1.anode
  N6: R2.Pin_1, LED5.anode
  N7: R3.Pin_1, LED4.anode

notes:
  En este proyecto se ha incorporado un buzzer que produce sonidos. Se ha incorporado al proyecto tres leds, las que parparean al producirse los sonidos del buzzer.
  Componentes
  -Placa Arduino Uno
  -Un buzzer
  -Tres leds
  -Tres resistencias de 200 ohmios.
  -Breadboard
  TÍTULO DEL PROYECTO
  "AVISO DE PASE LA PISTA PARA INVIDENTES"
  DESCRIPCIÓN DEL PROYECTO.
  Se enciende primero la luz verde.
  Inmediatamente se enciende la luz amarilla que es aviso al pase de la luz roja con sonido.
  Cuando la luz roja, led de color rojo se enciende, inmediatamente suena el buzzer, y la persona invidente se detiene.
