# Fritzing sketch id3632_SemaforoProyecto_0 (saved by Fritzing 0.9.3b)
breadboards: 1

parts:
  LED1 = LED - 5mm [color="Red (633nm)" package="5 mm [THT]"]
  LED2 = LED - 5mm [color="Red (633nm)" package="5 mm [THT]"]
  LED3 = LED - 5mm [color="Red (633nm)" package="5 mm [THT]"]
  R1 = Resistor [tolerance=±5% resistance=220 package=THT]
  R2 = Resistor [tolerance=±5% resistance=220 package=THT]
  R3 = Resistor [tolerance=±5% resistance=220 package=THT]
  hc-sr1 = hc-sr04
  Componente1 = Arduino Mega 2560 (Rev3)

nets:
  N1: LED1.cathode, R1.Pin_0
  N2: LED1.anode, Componente1.D10_PWM
  N3: LED2.cathode, R2.Pin_0
  N4: LED2.anode, Componente1.D9_PWM
  N5: LED3.cathode, R3.Pin_0
  N6: LED3.anode, Componente1.D8_PWM
  GND: R1.Pin_1, R2.Pin_1, R3.Pin_1, hc-sr1.GND, Componente1.GND
  VCC: hc-sr1.VCC, Componente1.5V
  N7: hc-sr1.Trig, hc-sr1.Echo, Componente1.D2_PWM, Componente1.D3_PWM
