# Fritzing sketch id3633_Trabajo_Fritzing_Papa_Bueno_0 (saved by Fritzing 0.9.3b)
breadboards: 1

parts:
  LED1 = LED - 5mm [color="Red (633nm)" package="5 mm [THT]"]
  LED2 = LED - 5mm [color="Yellow (595nm)" package="5 mm [THT]"]
  J1 = Piezo Speaker
  Componente1 = Arduino Uno (Rev3)
  R1 = Resistor [tolerance=±5% resistance=220 package=THT]
  R2 = Resistor [tolerance=±5% resistance=220 package=THT]

nets:
  N1: LED1.cathode, LED2.cathode, J1.pin1, Componente1.GND
  N2: LED1.anode, R2.Pin_1
  N3: LED2.anode, R1.Pin_1
  N4: J1.pin2, Componente1.D9_PWM
  N5: Componente1.D8, R1.Pin_0
  N6: Componente1.D7, R2.Pin_0

notes:
  [circuito de semaforo con sonido ]
