# Fritzing sketch id3634_cruce_de_semaforos._0 (saved by Fritzing 0.9.3b)
breadboards: 1

parts:
  Componente1 = Arduino Uno (Rev3)
  S1 = Pushbutton [package="[THT]"]
  R1 = Resistor [tolerance=±5% resistance=220 package=THT]
  R2 = Resistor [tolerance=±5% resistance=220 package=THT]
  R3 = Resistor [tolerance=±5% resistance=220 package=THT]
  R4 = Resistor [tolerance=±5% resistance=220 package=THT]
  R5 = Resistor [tolerance=±5% resistance=220 package=THT]
  R6 = Resistor [tolerance=±5% resistance=220 package=THT]
  LED1 = LED - 5mm [color="Red (633nm)" package="5 mm [THT]"]
  LED2 = LED - 5mm [color="Yellow (595nm)" package="5 mm [THT]"]
  LED3 = LED - 5mm [color="Yellow (595nm)" package="5 mm [THT]"]
  LED4 = LED - 5mm [color="Red (633nm)" package="5 mm [THT]"]
  LED5 = LED - 3mm [color="Green (570nm)" package="3 mm [THT]"]
  LED6 = LED - 3mm [color="Green (570nm)" package="3 mm [THT]"]
  R7 = Resistor [tolerance=±5% resistance=220 package=THT]

nets:
  N1: Componente1.D8, Componente1.5V, S1.Pin_3, S1.Pin_4, R7.Pin_1
  N2: Componente1.D2, R6.Pin_0
  N3: Componente1.D3_PWM, R5.Pin_0
  N4: Componente1.D4, R4.Pin_0
  N5: Componente1.D5_PWM, R3.Pin_0
  N6: Componente1.D6_PWM, R2.Pin_0
  N7: Componente1.D7, R1.Pin_0
  N8: Componente1.GND, LED1.cathode, LED2.cathode, LED3.cathode, LED4.cathode, LED6.cathode, R7.Pin_0
  N9: S1.Pin_1, S1.Pin_2
  N10: R1.Pin_1, LED1.anode
  N11: R2.Pin_1, LED2.anode
  N12: R3.Pin_1, LED6.anode
  N13: R4.Pin_1, LED4.anode
  N14: R5.Pin_1, LED3.anode
  N15: R6.Pin_1, LED5.anode
