# Fritzing sketch id3636_semaforo_programado_0 (saved by Fritzing 0.9.2b)
breadboards: 1

parts:
  Parte1 = Arduino Uno (Rev3)
  R1 = Resistor [tolerance=±5% resistance=220 package=THT]
  LED1 = LED - 5mm [color="Red (633nm)" package="5 mm [THT]"]
  R2 = Resistor [tolerance=±5% resistance=220 package=THT]
  R3 = Resistor [tolerance=±5% resistance=220 package=THT]
  LED2 = LED - 5mm [color="Yellow (585nm)" package="5 mm [THT]"]
  LED3 = LED - 5mm [color="Green (555nm)" package="5 mm [THT]"]

nets:
  N1: Parte1.D4, LED3.anode
  N2: Parte1.D5_PWM, LED2.anode
  N3: Parte1.D6_PWM, LED1.anode
  N4: Parte1.GND, R1.Pin_1, R2.Pin_1, R3.Pin_1
  N5: R1.Pin_0, LED1.cathode
