# Fritzing sketch id3637_codigoSemaforo_0 (saved by Fritzing 0.9.3b)
breadboards: 1

parts:
  LED1 = LED - 5mm [color="Yellow (595nm)" package="5 mm [THT]"]
  LED2 = LED - 5mm [color="Red (633nm)" package="5 mm [THT]"]
  LED3 = LED - 5mm [color="Green (555nm)" package="5 mm [THT]"]
  R1 = Resistor [tolerance=±5% resistance=220 package=THT]
  R2 = Resistor [tolerance=±5% resistance=220 package=THT]
  R3 = Resistor [tolerance=±5% resistance=220 package=THT]
  Componente1 = Arduino Uno (Rev3)

nets:
  N1: LED1.cathode, LED2.cathode, LED3.cathode, Componente1.GND
  N2: LED1.anode, R2.Pin_1
  N3: LED2.anode, R3.Pin_1
  N4: LED3.anode, R1.Pin_1
  N5: R1.Pin_0, R2.Pin_0, R3.Pin_0, Componente1.D2, Componente1.D4, Componente1.D6_PWM, Componente1.5V
