# Fritzing sketch id3638_Untitled_Sketch_9_0 (saved by Fritzing 0.9.2b)
breadboards: 1

parts:
  Parte2 = Arduino Uno (Rev3)
  LED12 = smd LED [color="Yellow (585nm)" package="1206 [SMD]"]
  LED13 = smd LED [color="Green (555nm)" package="1206 [SMD]"]
  R1 = Resistor [tolerance=±5% resistance=220 package=THT]
  LED15 = LED - 5mm [color="Red (633nm)" package="5 mm [THT]"]
  R4 = Resistor [tolerance=±5% resistance=220 package=THT]
  R5 = Resistor [tolerance=±5% resistance=220 package=THT]

nets:
  N1: Parte2.D4, LED15.anode
  N2: Parte2.D5_PWM, LED12.anode
  N3: Parte2.D6_PWM, LED13.anode
  N4: Parte2.GND, R1.Pin_1, R4.Pin_1, R5.Pin_1
  N5: LED12.cathode, R4.Pin_0
  N6: LED13.cathode, R5.Pin_0
  N7: R1.Pin_0, LED15.cathode
