# Fritzing sketch id3639_Semaforo_simples_0 (saved by Fritzing 0.7.12b)
breadboards: 1

parts:
  LED1 = LED - 5mm [color="Yellow (595nm)" package="5 mm [THT]"]
  LED2 = LED - 5mm [color="Green (555nm)" package="5 mm [THT]"]
  LED3 = LED - 5mm [color="Red (633nm)" package="5 mm [THT]"]
  R2 = Resistor [tolerance=±5% resistance=1k package=THT]
  R3 = Resistor [tolerance=±5% resistance=1k package=THT]
  Arduino1 = Arduino
  R4 = Resistor [tolerance=±5% resistance=1k package=THT]

nets:
  N1: LED1.cathode, LED2.cathode, LED3.cathode, Arduino1.GND
  N2: LED1.anode, R2.Pin_0
  N3: LED2.anode, R3.Pin_0
  N4: LED3.anode, R4.Pin_0
  N5: R2.Pin_1, Arduino1.D4
  N6: R3.Pin_1, Arduino1.D2
  N7: Arduino1.D6, R4.Pin_1
