# Fritzing sketch id363_ProjectPaintball_0 (saved by Fritzing 0.9.2b)
circuit board: 8.2495cm x 2.78161cm
breadboards: 1

parts:
  Part1 = Arduino Nano (Rev3.0)
  Solenoid = Solenoid
  Q1 = LTR-301 [package=ltr-301]  # not connected
  Mosfet = MOSFET-NCHANNEL [package=to220v]
  D1 = Diode [package=diode-hv]
  R1 = Resistor [tolerance=±5% resistance=10k package="1206 [SMD]"]
  LCD1 = LCD screen
  R2 = Resistor [tolerance=±5% resistance=220 package=THT]
  R3 = Trimmer Potentiometer [maximum_resistance=10kΩ package=THT]
  S2 = Pushbutton [package="[THT]"]
  S3 = Pushbutton [package="[THT]"]
  S4 = Pushbutton [package="[THT]"]
  R4 = Resistor [tolerance=±5% resistance=220 package=THT]
  R5 = Resistor [tolerance=±5% resistance=220 package=THT]
  R6 = Resistor [tolerance=±5% resistance=220 package=THT]

nets (from the breadboard view):
  GND: Part1.GND, R1.Pin_1, LCD1.VSS, LCD1.R/W, LCD1.LED-, R3.leg2, R4.Pin_0, R5.Pin_0, R6.Pin_1
  N1: Part1.D2, LCD1.DB7
  N2: Part1.D3, LCD1.DB6
  N3: Part1.D4, LCD1.DB5
  N4: Part1.D5, LCD1.DB4
  N5: Part1.D6, LCD1.E
  N6: Part1.D7, LCD1.RS
  N7: Part1.D8, S2.Pin_1, S2.Pin_2, R4.Pin_1
  N8: Part1.D9, S3.Pin_1, S3.Pin_2, R5.Pin_1
  N9: Part1.D10, S4.Pin_1, S4.Pin_2, R6.Pin_0
  N10: Part1.D11/MOSI, Mosfet.G, R1.Pin_0
  5V: Part1.5V, LCD1.VDD, R2.Pin_0, R3.leg1, S2.Pin_3, S2.Pin_4, S3.Pin_3, S3.Pin_4, S4.Pin_3, S4.Pin_4
  N11: Solenoid.pin1, Mosfet.D, D1.A
  N12: Solenoid.pin2, Mosfet.S, D1.C
  N13: LCD1.V0, R3.wiper
  N14: LCD1.LED+, R2.Pin_1
