# Fritzing sketch id3640_semaforo_0 (saved by Fritzing 0.7.5b)
breadboards: 1

parts:
  LED1 = LED - 5mm [color="Red (633nm)" package="5 mm [THT]"]
  R2 = Resistor [tolerance=±5% resistance=220 package=THT]
  Arduino1 = Arduino
  R4 = Resistor [tolerance=±5% resistance=220 package=THT]
  LED2 = LED - 5mm [color="Red (633nm)" package="5 mm [THT]"]
  LED3 = LED - 5mm [color="Red (633nm)" package="5 mm [THT]"]
  R5 = Resistor [tolerance=±5% resistance=220 package=THT]

nets:
  N1: LED1.cathode, R2.Pin_0
  N2: R2.Pin_1, Arduino1.GND, R4.Pin_1, R5.Pin_1
  N3: Arduino1.D8, LED2.anode
  N4: Arduino1.D6, LED3.anode
  N5: R4.Pin_0, LED2.cathode
  N6: LED3.cathode, R5.Pin_0
