# Fritzing sketch id3641_base_arduino_LEDS_EDUBASICA_0 (saved by Fritzing 0.9.3b)
breadboards: 1

parts:
  Componente1 = Arduino Uno (Rev3)
  LED1 = LED - 5mm [color="Green (570nm)" package="5 mm [THT]"]
  R1 = Resistor [tolerance=±5% resistance=220 package=THT]
  LED2 = LED - 5mm [color="Yellow (595nm)" package="5 mm [THT]"]
  R2 = Resistor [tolerance=±5% resistance=220 package=THT]
  LED3 = LED - 5mm [color="Red (633nm)" package="5 mm [THT]"]
  R3 = Resistor [tolerance=±5% resistance=220 package=THT]

nets:
  N1: Componente1.GND, R1.Pin_1, R2.Pin_1, R3.Pin_1
  N2: Componente1.D3_PWM, LED1.cathode
  N3: Componente1.D4, LED2.cathode
  N4: Componente1.D5_PWM, LED3.cathode
  N5: LED1.anode, R1.Pin_0
  N6: LED2.anode, R2.Pin_0
  N7: LED3.anode, R3.Pin_0
