# Fritzing sketch id3642_Semaforo_0 (saved by Fritzing 0.7.0b)
breadboards: 1

parts:
  Arduino1 = Arduino
  LED1 = LED - 5mm [color="Red (633nm)" package="5 mm [THT]"]
  LED2 = LED - 5mm [color="Green (560nm)" package="5 mm [THT]"]
  R1 = Resistor [tolerance=±5% resistance=220 package=THT]
  R3 = Resistor [tolerance=±5% resistance=220 package=THT]

nets:
  N1: Arduino1.D7, R1.Pin_0
  N2: Arduino1.D4, R3.Pin_0
  N3: Arduino1.GND, LED1.cathode, LED2.cathode
  N4: LED1.anode, R1.Pin_1
  N5: LED2.anode, R3.Pin_1
