# Fritzing sketch id3643_SEMAFORO_CARDENAS_0 (saved by Fritzing 0.9.3b)
breadboards: 1

parts:
  LED1 = LED - 5mm [color="Red (633nm)" package="5 mm [THT]"]
  LED2 = LED - 5mm [color="Yellow (595nm)" package="5 mm [THT]"]
  LED3 = LED - 5mm [color="Green (570nm)" package="5 mm [THT]"]
  R1 = Resistor [tolerance=±5% resistance=330 package=THT]
  R2 = Resistor [tolerance=±5% resistance=330 package=THT]
  R3 = Resistor [tolerance=±5% resistance=330 package=THT]
  Componente1 = Arduino Ethernet Shield (Rev3)

nets:
  N1: LED1.cathode, R3.Pin_1
  N2: LED2.cathode, R1.Pin_1
  N3: LED3.cathode, R2.Pin_1
  N4: R1.Pin_0, Componente1.PWM_D5
  N5: R2.Pin_0, Componente1.D7
  N6: R3.Pin_0, Componente1.PWM_D3

notes:
  PROYECTO SEMAFORO
  CARDENAS JOSE
