# Fritzing sketch id3645_Semaforo_clavero_0 (saved by Fritzing 0.9.3b)
breadboards: 1

parts:
  Componente1 = Arduino Uno (Rev3)
  R1 = Resistor [tolerance=±5% resistance=220 package=THT]
  R2 = Resistor [tolerance=±5% resistance=220 package=THT]
  R3 = Resistor [tolerance=±5% resistance=220 package=THT]
  LED1 = LED - 5mm [color="Green (555nm)" package="5 mm [THT]"]
  LED2 = LED - 5mm [color="Yellow (585nm)" package="5 mm [THT]"]
  LED3 = LED - 5mm [color="Red (633nm)" package="5 mm [THT]"]

nets:
  N1: Componente1.D8, R3.Pin_1
  N2: Componente1.D9_PWM, R2.Pin_1
  N3: Componente1.D10_PWM/SS, R1.Pin_1
  N4: Componente1.GND, LED1.cathode, LED2.cathode, LED3.cathode
  N5: R1.Pin_0, LED1.anode
  N6: R2.Pin_0, LED2.anode
  N7: R3.Pin_0, LED3.anode
