# Fritzing sketch id3648_pt1000_Sketch_0 (saved by Fritzing 0.8.7b)
circuit board: 8.46667cm x 5.64444cm
breadboards: 1

parts:
  R1 = Temperature Sensor (Thermistor) [thermistor_type=NTC package=THT]
  R2 = Resistor [tolerance=±5% resistance=10k package=THT]
  R3 = Rotary Potentiometer (Small) [maximum_resistance=10kΩ package=THT]
  R4 = Resistor [tolerance=±5% resistance=100k package=THT]
  R5 = Resistor [tolerance=±5% resistance=10k package=THT]
  R6 = Resistor [tolerance=±5% resistance=10k package=THT]
  R8 = Resistor [tolerance=±5% resistance=56k package=THT]
  R9 = Resistor [tolerance=±5% resistance=56k package=THT]
  R10 = Resistor [tolerance=±5% resistance=220k package=THT]
  LM324N1 = LM324N

nets:
  N1: R1.pin_0, R3.wiper, R9.Pin_1, LM324N1.connector10
  N2: R1.pin_1, R2.Pin_1, LM324N1.connector2
  N3: R2.Pin_0, R4.Pin_0, R10.Pin_0, LM324N1.connector3
  N4: R3.leg1, R4.Pin_1, LM324N1.connector4
  N5: R5.Pin_0, R6.Pin_0, R8.Pin_1, R9.Pin_0, LM324N1.connector11, LM324N1.connector12
  N6: R5.Pin_1, LM324N1.connector0, LM324N1.connector1
  N7: R6.Pin_1, LM324N1.connector5, LM324N1.connector6
  N8: R8.Pin_0, R10.Pin_1, LM324N1.connector13
