# Fritzing sketch id3649_semaforo_0 (saved by Fritzing 0.9.2b)
breadboards: 1

parts:
  Parte1 = Arduino Uno (Rev3)
  R1 = Resistor [tolerance=±5% resistance=220 package=THT]
  LED1 = LED - 5mm [color="Red (633nm)" package="5 mm [THT]"]
  LED2 = LED - 5mm [color="Yellow (595nm)" package="5 mm [THT]"]
  LED3 = LED - 5mm [color="Green (570nm)" package="5 mm [THT]"]
  R2 = Resistor [tolerance=±5% resistance=220 package=THT]
  R3 = Resistor [tolerance=±5% resistance=220 package=THT]
  VCC1 = Battery

nets:
  N1: Parte1.D8, R3.Pin_0
  N2: Parte1.D6_PWM, R1.Pin_0
  N3: Parte1.D7, R2.Pin_0
  N4: Parte1.5V, VCC1.+
  N5: Parte1.GND, R1.Pin_1, LED1.cathode, LED2.cathode, LED3.cathode, VCC1.-
  N6: LED1.anode, LED3.anode, R3.Pin_1
  N7: LED2.anode, R2.Pin_1
