# Fritzing sketch id364_Arbol_0 (saved by Fritzing 0.8.0b)

parts:
  Parte1 = Arduino Uno (Rev3)
  LED1 = Super Flux RGB LED (com. anode) [color=Blue part_number=WS2812B]
  LED2 = Super Flux RGB LED (com. anode) [color=Blue part_number=WS2812B]
  LED3 = Super Flux RGB LED (com. anode) [color=Blue part_number=WS2812B]
  LED4 = Super Flux RGB LED (com. anode) [color=Blue part_number=WS2812B]
  LED5 = Super Flux RGB LED (com. anode) [color=Blue part_number=WS2812B]
  C1 = Ceramic Capacitor [capacitance=100nF package="100 mil [THT, multilayer]"]
  C2 = Ceramic Capacitor [capacitance=100nF package="100 mil [THT, multilayer]"]  # not connected
  C3 = Ceramic Capacitor [capacitance=100nF package="100 mil [THT, multilayer]"]  # not connected
  J1 = Piezo Speaker
  LED20 = Super Flux RGB LED (com. anode) [color=Blue part_number=WS2812B]
  C4 = Ceramic Capacitor [capacitance=100nF package="100 mil [THT, multilayer]"]  # not connected

nets:
  N1: Parte1.A0, J1.pin2
  N2: Parte1.A1, LED1.common_anode
  N3: Parte1.GND, J1.pin1
  N4: LED1.red_cathode, LED5.red_cathode, C1.0, LED20.red_cathode
  N5: LED1.blue_cathode, LED2.common_anode
  N6: LED1.green_cathode, LED5.green_cathode
  N7: LED2.blue_cathode, LED3.common_anode
  N8: LED3.blue_cathode, LED4.common_anode
  N9: LED4.blue_cathode, LED5.common_anode
  N10: LED5.blue_cathode, LED20.common_anode
