# Fritzing sketch id3651_Semaphore_0 (saved by Fritzing 0.9.2b)
breadboards: 1

parts:
  Raspberry_Pi1 = Raspberry Pi B+
  R1 = Resistor [tolerance=±5% resistance=220 package="0603 [SMD]"]
  R2 = Resistor [tolerance=±5% resistance=220 package="0603 [SMD]"]
  R3 = Resistor [tolerance=±5% resistance=220 package="0603 [SMD]"]
  LED1 = smd LED [color="Green (555nm)" package="0603 [SMD]"]
  LED2 = smd LED [color="Yellow (595nm)" package="0603 [SMD]"]
  LED3 = smd LED [color="Red (635nm)" package="0603 [SMD]"]

nets:
  N1: Raspberry_Pi1.GND, LED1.cathode, LED2.cathode, LED3.cathode
  N2: Raspberry_Pi1.GPIO21, R2.Pin_0
  N3: Raspberry_Pi1.GPIO20, R1.Pin_0
  N4: Raspberry_Pi1.GPIO16, R3.Pin_0
  N5: R1.Pin_1, LED2.anode
  N6: R2.Pin_1, LED1.anode
  N7: R3.Pin_1, LED3.anode
