# Fritzing sketch id3652_Senior_Design_0 (saved by Fritzing 0.9.3b)
breadboards: 1

parts:
  J1 = Basic Servo
  J2 = Basic Servo
  J3 = Basic Servo
  Part1 = Arduino Uno (Rev3)
  SP1 = SPEAKER [package=pcb_mount_speaker]

nets:
  GND: J1.gnd, J2.gnd, J3.gnd, Part1.D9_PWM, Part1.GND, SP1.-
  VCC: J1.vcc, J2.vcc, J3.vcc, Part1.5V, SP1.+
  N1: J1.pulse, J2.pulse, Part1.D6_PWM
  N2: J3.pulse, Part1.D5_PWM
