# Fritzing sketch id3653_senior_design_0 (saved by Fritzing 0.9.3b)
breadboards: 1

parts:
  Part1 = Humidity Sensor - HIH-4030 Breakout  # not connected
  Part2 = Logic Level Converter  # not connected
  Part3 = Arduino ProtoShield  # not connected
  Parts1 = prefix0000_DEV-12757_03 [part_number=DEV-12757]
  U1 = LCD-16X2 [package=lcd-16x2]  # not connected

nets:
  N1: Parts1.connector87, Parts1.connector89
