# Fritzing sketch id3655_senior_design_wired_0 (saved by Fritzing 0.9.3b)

parts:
  Part1 = Humidity Sensor - HIH-4030 Breakout
  Part2 = Logic Level Converter
  Part3 = Arduino ProtoShield
  Parts1 = prefix0000_DEV-12757_03 [part_number=DEV-12757]
  U1 = LCD-16X2 [package=lcd-16x2]  # not connected
  Part4 = Digital Temperature Sensor Breakout - TMP102

nets:
  GND: Part1.GND, Part2.GND, Part3.GND, Part3.N$100, Part3.N$104, Parts1.connector89, Part4.GND
  N1: Part1.OUT, Part3.A0
  VCC: Part1.VCC, Part2.HV, Part3.5V, Part3.N$89, Parts1.connector87
  N2: Part2.TX2_LV, Part3.N$126, Part4.SCL
  N3: Part2.RX2_LV, Part3.N$115, Part4.SDA
  N4: Part2.LV, Part3.N$93, Part4.V+
  N5: Part2.RX_LV, Part3.N$82
  N6: Part2.TX_LV, Part3.N$71, Part4.ALERT
  N7: Part2.TX_HV, Part3.A3, Part3.N$67
  N8: Part2.RX_HV, Part3.N$78
  N9: Part2.RX2_HV, Part3.A4, Part3.N$111
  N10: Part2.TX2_HV, Part3.A5, Part3.N$122
