# Fritzing sketch id3656_SeniorDesign_0 (saved by Fritzing 0.9.3b)
breadboards: 2

parts:
  Part1 = Arduino Mega 2560 (Rev3)
  Part3 = Motor Driver 1A Dual TB6612FNG
  BAT1 = BC9VPC [package=bc9vpc]
  Q2 = Basic FET N-Channel [package="D2Pak [SMD]"]
  D1 = Zener Diode [part_number=1N4732A breakdown_voltage=3.6V package="300 mil [THT]"]
  M1 = DC Motor
  R1 = Resistor [tolerance=±5% resistance=220 package="0603 [SMD]"]
  L1 = Solenoid
  R2 = Resistor [tolerance=±5% resistance=500 package=THT]
  R3 = Resistor [tolerance=±5% resistance=500 package=THT]
  D2 = Zener Diode [part_number=1N4732A breakdown_voltage=3.6V package="300 mil [THT]"]
  Q3 = Basic FET N-Channel [package="D2Pak [SMD]"]
  J1 = Basic Servo
  M2 = Stepper Motor - Bipolar
  BAT2 = BC9VPC [package=bc9vpc]
  Part4 = EasyDriver_v44
  RJ-1 = RJ-11 Connector with Breakout Board
  J3 = Basic Servo
  MPX4250AP1 = MPX4250AP pressure sensor [part_number=MPX]
  MPX4250AP2 = MPX4250AP pressure sensor [part_number=MPX]
  LCD1 = LCD screen
  U1 = POT [package=pot_mammoth]

nets:
  N1: Part1.A8, J3.pulse
  N2: Part1.A10, J1.pulse
  N3: Part1.A0, Part4.STEP
  N4: Part1.A5, MPX4250AP2.V_out
  N5: Part1.A6, MPX4250AP1.V_out
  N6: Part1.A7, RJ-1.PRB
  GND: Part1.GND, Part3.GND, BAT1.V-, Q2.source, Q3.source, J1.gnd, BAT2.V-, Part4.GND, RJ-1.GND, J3.gnd, MPX4250AP1.GND, MPX4250AP2.GND, LCD1.VSS, LCD1.R/W, U1.S
  N7: Part1.D10_PWM, LCD1.DB7
  N8: Part1.D9_PWM, LCD1.DB6
  N9: Part1.D8_PWM, LCD1.DB5
  VCC: Part1.5V, Part3.VCC, J1.vcc, RJ-1.Vcc, J3.vcc, MPX4250AP1.Vs, MPX4250AP2.Vs, LCD1.VDD
  N10: Part1.D2_PWM, Part3.PWMA
  N11: Part1.D3_PWM, Part3.PWMB
  N12: Part1.D5_PWM, LCD1.RS
  N13: Part1.D6_PWM, LCD1.E
  N14: Part1.D7_PWM, LCD1.DB4
  N15: Part1.D28, Part4.DIR
  N16: Part1.D47, Part3.BIN1
  N17: Part1.D49, Part3.STBY
  N18: Part1.D51, Part3.AIN1
  N19: Part3.B01, R1.Pin_1
  N20: Part3.A01, R2.Pin_0
  N21: Part3.VM, BAT1.V+, D1.cathode, M1.pin_1, L1.pin2, D2.cathode
  N22: Q2.Gate, R1.Pin_0
  N23: Q2.drain, D1.anode, M1.pin_2
  N24: L1.pin1, D2.anode, Q3.drain
  N25: R2.Pin_1, R3.Pin_1
  N26: R3.Pin_0, Q3.Gate
  N27: M2.A, Part4.OUT2A
  N28: M2.C, Part4.OUT2B
  N29: M2.B, Part4.OUT1A
  N30: M2.D, Part4.OUT1B
  N31: BAT2.V+, Part4.V+
  N32: LCD1.V0, U1.A

notes:
  12V Battery
  Diagpraghm Pump (12V DC)
  Solenoid Valve
  Flow Sensor
  Pinch Valve
  Pressure Relief Valve
  Pressure Sensor 1 & 2
  Stepper Motor for syringe
