# Fritzing sketch id3658_sensitive_wearable_1_0 (saved by Fritzing 0.9.1b)

parts:
  Part1 = LilyPad Arduino Simple Board
  R1 = Basic Flex Resistor
  J1 = Basic Force Sensing Resistor (FSR) [package=THT]
  J2 = Basic Force Sensing Resistor (FSR) [package=THT]
  Part2 = LilyPad Tri-Color LED
  R2 = Resistor [tolerance=±5% resistance=10k package=THT]
  R3 = Resistor [tolerance=±5% resistance=10k package=THT]
  R4 = Resistor [tolerance=±5% resistance=10k package=THT]

nets:
  N1: Part1.A2, J2.pin_0, R3.Pin_1
  N2: Part1.A3, R1.pin_1, R4.Pin_1
  N3: Part1.A5, J1.pin_1, R2.Pin_0
  N4: Part1.D11, Part2.R
  N5: Part1.D9, Part2.G
  N6: Part1.D10, Part2.B
  N7: Part1.GND, R2.Pin_1, R3.Pin_0, R4.Pin_0
  N8: Part1.VCC, R1.Pin_2, J1.pin_0, J2.pin_1, Part2.+
