# Fritzing sketch id3659_SensorDetector_0 (saved by Fritzing 0.9.2b)
breadboards: 1

parts:
  R1 = Resistor [tolerance=±10% resistance=330 package=THT]
  R2 = Resistor [tolerance=±10% resistance=330 package=THT]
  R3 = Resistor [tolerance=±10% resistance=330 package=THT]
  R4 = Resistor [tolerance=±10% resistance=330 package=THT]
  R5 = Resistor [tolerance=±10% resistance=330 package=THT]
  R6 = Resistor [tolerance=±10% resistance=330 package=THT]
  R7 = Resistor [tolerance=±10% resistance=330 package=THT]
  R8 = Resistor [tolerance=±10% resistance=330 package=THT]
  U2 = 74HC595 [package="DIP16 [THT]"]
  R9 = Resistor [tolerance=±5% resistance=2.2k package=THT]
  R11 = Resistor [tolerance=±5% resistance=2.2k package=THT]
  R12 = Resistor [tolerance=±5% resistance=2.2k package=THT]
  S1 = Momentary Switch [package=ksa_sealed_tac_switch]
  7_Segment5 = 7 Segment Display
  7_Segment6 = 7 Segment Display
  7_Segment7 = 7 Segment Display
  U1 = atmega168 [package=dip]
  R13 = Resistor [tolerance=±5% resistance=10k package=THT]
  Q2 = PNP-Transistor [part_number=S8550 package="TO92 [THT]"]
  Q3 = PNP-Transistor [part_number=S8550 package="TO92 [THT]"]
  Q4 = PNP-Transistor [part_number=S8550 package="TO92 [THT]"]
  Q5 = NPN-Transistor [part_number=BC547 package="TO92 [THT]"]
  LED1 = LEDs [package=led10mm]
  R14 = Resistor [tolerance=±5% resistance=330 package=THT]
  J1 = Piezo Speaker
  R15 = TRIMPOT [package=3362u-2]
  U3 = SWITCH_SPDT [package=kps-1290]
  R16 = Resistor [tolerance=±5% resistance=220 package=THT]
  U4 = GAS_SENSOR [package=mq-3]  # not connected
  Part1 = Gas Sensor Breakout Board  # not connected

nets:
  N1: R1.Pin_0, 7_Segment5.Segment_F, 7_Segment6.Segment_F, 7_Segment7.Segment_F
  N2: R1.Pin_1, U2.Q5
  N3: R2.Pin_0, 7_Segment5.Segment_A, 7_Segment6.Segment_A, 7_Segment7.Segment_A
  N4: R2.Pin_1, U2.Q6
  N5: R3.Pin_0, 7_Segment5.Segment_B, 7_Segment6.Segment_B, 7_Segment7.Segment_B
  N6: R3.Pin_1, U2.Q7
  N7: R4.Pin_0, 7_Segment5.Segment_G, 7_Segment6.Segment_G, 7_Segment7.Segment_G
  N8: R4.Pin_1, U2.Q4
  N9: R5.Pin_0, 7_Segment5.Segment_DP, 7_Segment6.Segment_DP, 7_Segment7.Segment_DP
  N10: R5.Pin_1, U2.Q0
  N11: R6.Pin_0, 7_Segment5.Segment_C, 7_Segment6.Segment_C, 7_Segment7.Segment_C
  N12: R6.Pin_1, U2.Q1
  N13: R7.Pin_0, 7_Segment5.Segment_D, 7_Segment6.Segment_D, 7_Segment7.Segment_D
  N14: R7.Pin_1, U2.Q2
  N15: R8.Pin_0, 7_Segment5.Segment_E, 7_Segment6.Segment_E, 7_Segment7.Segment_E
  N16: R8.Pin_1, U2.Q3
  GND: U2.GND, U2.OE, U1.GND, Q2.C, Q3.C, Q4.C, J1.pin1, R15.CCW, U3.O
  VCC: U2.MR, U2.VCC, U1.VCC, U1.AVCC, R13.Pin_1, Q5.C, R14.Pin_1, R15.CW, R16.Pin_0
  N17: U2.SH_CP, U1.D9_(PWM)
  N18: U2.ST_CP, U1.D10_(PWM)
  N19: U2.DS, U1.D11_(PWM)
  N20: R9.Pin_0, Q2.B
  N21: R9.Pin_1, U1.D2
  N22: R11.Pin_0, Q4.B
  N23: R11.Pin_1, U1.D4
  N24: R12.Pin_0, Q3.B
  N25: R12.Pin_1, U1.D3_(PWM)
  N26: S1.1, S1.2, U1.RESET, R13.Pin_0
  N27: S1.3, S1.4
  N28: 7_Segment5.common_anode, Q4.E
  N29: 7_Segment6.common_anode, Q3.E
  N30: 7_Segment7.common_anode, Q2.E
  N31: U1.XLAT1, Q5.B
  N32: U1.A1, U3.P
  N33: U1.A3, R15.WIPER
  N34: Q5.E, LED1.C, J1.pin2
  N35: LED1.A, R14.Pin_0
  N36: U3.S, R16.Pin_1

notes:
  Analog sensor goes <--here; ground,
  power and analog
  input.
