# Fritzing sketch id3662_CircuitoTCC_0 (saved by Fritzing 0.9.3b)
breadboards: 1

parts:
  Arduino2 = Arduino Uno (Rev3)
  Componente1 = Bluetooth HC-05 Macho
  LED1 = smd LED [color="Infrared (850nm)" package="0603 [SMD]"]
  LED2 = smd LED [color="Infrared (850nm)" package="0603 [SMD]"]
  LED3 = smd LED [color="Infrared (850nm)" package="0603 [SMD]"]
  LED4 = smd LED [color="Infrared (850nm)" package="0603 [SMD]"]
  LED5 = smd LED [color="Infrared (850nm)" package="0603 [SMD]"]
  LED6 = smd LED [color="Infrared (850nm)" package="0603 [SMD]"]
  LED7 = smd LED [color="Infrared (850nm)" package="0603 [SMD]"]
  LED8 = smd LED [color="Infrared (850nm)" package="0603 [SMD]"]
  LED9 = smd LED [color="Infrared (850nm)" package="0603 [SMD]"]
  LED10 = smd LED [color="Infrared (850nm)" package="0603 [SMD]"]
  LED11 = smd LED [color="Infrared (850nm)" package="0603 [SMD]"]
  LED12 = smd LED [color="Infrared (850nm)" package="0603 [SMD]"]
  R1 = Resistor [tolerance=±5% resistance=220 package="0402 [SMD]"]
  R2 = Resistor [tolerance=±5% resistance=220 package="0402 [SMD]"]
  R3 = Resistor [tolerance=±5% resistance=220 package="0402 [SMD]"]
  R4 = Resistor [tolerance=±5% resistance=220 package="0402 [SMD]"]
  R5 = Resistor [tolerance=±5% resistance=220 package="0402 [SMD]"]
  R6 = Resistor [tolerance=±5% resistance=220 package="0402 [SMD]"]
  R7 = Resistor [tolerance=±5% resistance=220 package="0402 [SMD]"]
  R8 = Resistor [tolerance=±5% resistance=220 package="0402 [SMD]"]
  R9 = Resistor [tolerance=±5% resistance=220 package="0402 [SMD]"]
  R10 = Resistor [tolerance=±5% resistance=220 package="0402 [SMD]"]
  R11 = Resistor [tolerance=±5% resistance=220 package="0402 [SMD]"]
  R12 = Resistor [tolerance=±5% resistance=220 package="0402 [SMD]"]

nets:
  N1: Arduino2.D8, LED6.anode
  N2: Arduino2.D9_PWM, LED5.anode
  N3: Arduino2.D10_PWM/SS, LED4.anode
  N4: Arduino2.D11_PWM/MOSI, LED3.anode
  N5: Arduino2.D12/MISO, LED2.anode
  N6: Arduino2.D13/SCK, LED1.anode
  GND: Arduino2.GND, Componente1.GND, R1.Pin_0, R2.Pin_0, R3.Pin_0, R4.Pin_0, R5.Pin_0, R6.Pin_0, R7.Pin_0, R8.Pin_0, R9.Pin_0, R10.Pin_0, R11.Pin_0, R12.Pin_0
  N7: Arduino2.D0/RX, Componente1.TXD
  N8: Arduino2.D1/TX, Componente1.RXD
  N9: Arduino2.D2, LED12.anode
  N10: Arduino2.D3_PWM, LED11.anode
  N11: Arduino2.D4, LED10.anode
  N12: Arduino2.D5_PWM, LED9.anode
  N13: Arduino2.D6_PWM, LED8.anode
  N14: Arduino2.D7, LED7.anode
  5V: Arduino2.5V, Componente1.VCC
  N15: LED1.cathode, R10.Pin_1
  N16: LED2.cathode, R9.Pin_1
  N17: LED3.cathode, R8.Pin_1
  N18: LED4.cathode, R1.Pin_1
  N19: LED5.cathode, R7.Pin_1
  N20: LED6.cathode, R2.Pin_1
  N21: LED7.cathode, R4.Pin_1
  N22: LED8.cathode, R5.Pin_1
  N23: LED9.cathode, R6.Pin_1
  N24: LED10.cathode, R3.Pin_1
  N25: LED11.cathode, R11.Pin_1
  N26: LED12.cathode, R12.Pin_1
