# Fritzing sketch id3663_Sensor_de_luz_omar_0 (saved by Fritzing 0.9.2b)
breadboards: 1

parts:
  Parte1 = Arduino Uno (Rev3)
  R1 = Rotary Potentiometer (Small) [maximum_resistance=100kΩ package=THT]
  LED1 = LED - 5mm [color="Red (633nm)" package="5 mm [THT]"]
  R2 = Resistor [tolerance=±5% resistance=220 package=THT]
  R3 = Resistor [tolerance=±5% resistance=1k package=THT]
  R4 = Resistor [tolerance=±5% resistance=1k package=THT]
  S1 = Pushbutton [package=THT]
  R5 = Photocell (LDR) [package=THT]

nets:
  N1: Parte1.A0, R4.Pin_0, R5.pin_0
  N2: Parte1.D8, R3.Pin_0, S1.leg0
  N3: Parte1.D12/MISO, LED1.anode
  N4: Parte1.GND, R1.leg1, R2.Pin_1, R3.Pin_1, R4.Pin_1
  N5: Parte1.5V, R1.leg2, S1.leg1, R5.pin_1
  N6: LED1.cathode, R2.Pin_0
