# Fritzing sketch id3666_Sensor_de_Temperatura_com_LCD_para_Arduino___DHT11_0 (saved by Fritzing 0.9.3b)
breadboards: 1

parts:
  Componente1 = Arduino Uno (Rev3)
  LCD1 = LCD screen
  R1 = Resistor [tolerance=±5% resistance=1k package=THT]
  R2 = Rotary Potentiometer (Small) [maximum_resistance=100kΩ package=THT]
  RHT1 = Humidity and Temperature Sensor RHT03
  R3 = Resistor [tolerance=±5% resistance=10k package=THT]

nets:
  N1: Componente1.D11_PWM/MOSI, LCD1.E
  N2: Componente1.D12/MISO, LCD1.RS
  N3: Componente1.D2, LCD1.DB7
  N4: Componente1.D3_PWM, LCD1.DB6
  N5: Componente1.D4, LCD1.DB5
  N6: Componente1.D5_PWM, LCD1.DB4
  N7: Componente1.D7, RHT1.GND_1, R3.Pin_1
  5V: Componente1.5V, LCD1.VDD, R1.Pin_0, R2.leg2, RHT1.Vcc, R3.Pin_0
  GND: Componente1.GND, LCD1.VSS, LCD1.R/W, LCD1.LED-, R2.leg1, RHT1.GND_2
  N8: LCD1.V0, R2.wiper
  N9: LCD1.LED+, R1.Pin_1
