# Fritzing sketch id3668_allera_pizo_electrico_0 (saved by Fritzing 0.9.3b)
circuit board: 5.36861cm x 6.88462cm
breadboards: 1

parts:
  LED1 = LED - 5mm [color="Blue (505nm)" package="5 mm [THT]"]
  R1 = Resistor [tolerance=±5% resistance=220 package=THT]
  R2 = Resistor [tolerance=±5% resistance=1M package=THT]
  J1 = Piezo Speaker
  Arduino1 = Arduino Uno (Rev3)

nets:
  N1: LED1.cathode, R2.Pin_1, J1.pin1, Arduino1.GND
  N2: LED1.anode, R1.Pin_1
  N3: R1.Pin_0, Arduino1.D9_PWM
  N4: R2.Pin_0, J1.pin2, Arduino1.A0
