# Fritzing sketch id3669_sensorGreen_0 (saved by Fritzing 0.9.2b)
breadboards: 1

parts:
  パーツ1 = Arduino Uno (Rev3)
  J1 = Infrared Proximity Sensor
  C1 = Ceramic Capacitor [capacitance=0.1nF package="100 mil [THT, multilayer]"]
  LED1 = LED - 5mm [color="Red (633nm)" package="5 mm [THT]"]
  LED2 = LED - 5mm [color="Green (555nm)" package="5 mm [THT]"]
  R1 = Resistor [tolerance=±5% resistance=100 package=THT]
  R2 = Resistor [tolerance=±5% resistance=100 package=THT]

nets:
  N1: パーツ1.A0, J1.Vout, C1.0, C1.1
  GND: パーツ1.GND, J1.GND, LED1.cathode, LED2.cathode
  N2: パーツ1.D6_PWM, R2.Pin_1
  N3: パーツ1.D7, R1.Pin_0
  5V: パーツ1.5V, J1.Vcc
  N4: LED1.anode, R2.Pin_0
  N5: LED2.anode, R1.Pin_1
