# Fritzing sketch id366_micro+enc_ON_OFF_0 (saved by Fritzing 0.9.3b)
breadboards: 1

parts:
  Componente1 = Arduino Micro (Rev3)
  Componente2 = richardbruneau000
  LED1 = LEDs [package=led10mm]
  R1 = Resistor [tolerance=±5% resistance=2.2k package="2010 [SMD]"]

nets:
  N1: Componente1.MOSI, Componente2.connector12
  N2: Componente1.RXLED/SS, Componente2.connector11
  N3: Componente1.SCK, Componente2.connector13
  N4: Componente1.MISO, Componente2.connector15
  N5: Componente1.GND, Componente2.connector9
  N6: Componente1.3V3, Componente2.connector8
  N7: LED1.A, R1.Pin_0
