# Fritzing sketch id3670_Detector_Infrarrojo._0 (saved by Fritzing 0.7.11b)
breadboards: 1

parts:
  R6 = Resistor [resistance=10k tolerance=±5% package=THT]
  Arduino1 = Arduino
  R7 = Resistor [resistance=10k tolerance=±5% package=THT]
  S1 = Pushbutton [package="[THT]"]
  R8 = Resistor [resistance=10k tolerance=±5% package=THT]
  I_R_Receptor = LED - 3mm [color="Infrared (940nm)" package="3 mm [THT]"]
  I_R_Emisor = LED - 3mm [color="Infrared (940nm)" package="3 mm [THT]"]
  LED5 = LED - 5mm [color="Red (633nm)" package="5 mm [THT]"]

nets:
  N1: R6.Pin_0, I_R_Emisor.cathode
  N2: R6.Pin_1, Arduino1.GND, R7.Pin_1, R8.Pin_1
  N3: Arduino1.D13, LED5.cathode
  N4: Arduino1.D12, LED5.anode
  N5: Arduino1.D3, I_R_Emisor.anode
  N6: Arduino1.D2, R7.Pin_0, S1.Pin_1, S1.Pin_2
  N7: Arduino1.+5V, S1.Pin_3, S1.Pin_4, I_R_Receptor.anode
  N8: Arduino1.A2, R8.Pin_0, I_R_Receptor.cathode
