# Fritzing sketch id3672_ldr_0 (saved by Fritzing 0.9.2b)
breadboards: 1

parts:
  R1 = Photocell (LDR) [package=THT]
  Parte1 = Arduino Uno (Rev3)
  R2 = Resistor [tolerance=±5% resistance=2.2k package=THT]

nets:
  N1: R1.pin_0, Parte1.A5/SCL, R2.Pin_1
  N2: R1.pin_1, Parte1.5V
  N3: Parte1.GND, R2.Pin_0
