# Fritzing sketch id3673_Sensor_LDR_3_niveis_0 (saved by Fritzing 0.7.11b)
breadboards: 1

parts:
  Arduino1 = Arduino
  R1 = Resistor [tolerance=±5% resistance=220 package=THT]
  R2 = Resistor [tolerance=±5% resistance=220 package=THT]
  R3 = Resistor [tolerance=±5% resistance=220 package=THT]
  R4 = Resistor [tolerance=±5% resistance=10k package=THT]
  R5 = Photocell (LDR) [package=THT]
  LED1 = LED - 5mm [color="Yellow (595nm)" package="5 mm [THT]"]
  LED2 = LED - 5mm [color="Green (565nm)" package="5 mm [THT]"]
  LED3 = LED - 5mm [color="Orange (620nm)" package="5 mm [THT]"]

nets:
  N1: Arduino1.D13, LED3.anode
  N2: Arduino1.D12, LED2.anode
  N3: Arduino1.D11, LED1.anode
  N4: Arduino1.+5V, R5.pin_0
  N5: Arduino1.GND, R1.Pin_1, R2.Pin_1, R3.Pin_1, R4.Pin_1
  N6: Arduino1.A0, R4.Pin_0, R5.pin_1
  N7: R1.Pin_0, LED1.cathode
  N8: R2.Pin_0, LED3.cathode
  N9: R3.Pin_0, LED2.cathode

notes:
  LOW  MID   HIGH
