# Fritzing sketch id3675_Reading_IC_CNY70_as_digital_sensor (saved by Fritzing 0.9.3b)
breadboards: 1

parts:
  R1 = Resistor [tolerance=±5% resistance=220 package=THT]
  R2 = Resistor [tolerance=±5% resistance=10k package=THT]
  Componente1 = Arduino Uno (Rev3)
  IC1 = IC, DIP package, 4 pins [chip_label=IC]

nets:
  N1: R1.Pin_0, R2.Pin_0, Componente1.GND
  N2: R1.Pin_1, IC1.pin1
  N3: R2.Pin_1, Componente1.D10_PWM/SS, IC1.pin3
  N4: Componente1.5V, IC1.pin2, IC1.pin4
