# Fritzing sketch id3675_gfg_0 (saved by Fritzing 0.9.2b)
circuit board: 8.46667cm x 5.64444cm
breadboards: 2

parts:
  S1 = Pushbutton [package=THT]
  S2 = Pushbutton [package=THT]
  R2 = Rotary Potentiometer (Small) [maximum_resistance=100kΩ package=THT]
  Melikşah = Arduino Uno (Rev3)
  R3 = Resistor [tolerance=±5% resistance=220 package=THT]
  R4 = Resistor [tolerance=±5% resistance=220 package=THT]
  J2 = Infrared Proximity Sensor
  J1 = Piezo Speaker

nets:
  5V: S1.leg0, S1.leg1, S2.leg0, S2.leg1, Melikşah.D5_PWM, Melikşah.5V, R3.Pin_1, R4.Pin_1, J2.Vcc
  N1: R2.wiper, Melikşah.A0
  N2: Melikşah.D0/RX, J2.Vout
  N3: Melikşah.D3_PWM, J1.pin2
  GND: Melikşah.GND, R3.Pin_0, R4.Pin_0, J2.GND, J1.pin1
