# Fritzing sketch id3676_Sensor_Temperatura_0 (saved by Fritzing 0.9.2b)
breadboards: 1

parts:
  Componente1 = Arduino Uno (Rev3)
  RHT1 = Humidity and Temperature Sensor RHT03

nets:
  N1: Componente1.A1, RHT1.Data-signal
  5V: Componente1.5V, RHT1.Vcc
  N2: Componente1.GND, RHT1.GND_2
