# Fritzing sketch id3677_Ultrasonic_Sketch_0 (saved by Fritzing 0.9.2b)

parts:
  U1 = generic_sip_4_300mil.fzp [chip_label=IC]
  Componente1 = Arduino Uno (Rev3)

nets:
  N1: U1.connector0, Componente1.3V3
  N2: U1.connector1, Componente1.D7
  N3: U1.connector2, Componente1.D8
  N4: U1.connector3, Componente1.GND
