# Fritzing sketch id3678_Ultrasonido_0 (saved by Fritzing 0.9.2b)
breadboards: 1

parts:
  Componente2 = Arduino Uno (Rev3)
  U2 = generic_sip_4_300mil.fzp [chip_label=IC]

nets:
  N1: Componente2.D12/MISO, U2.connector1
  N2: Componente2.D13/SCK, U2.connector2
