# Fritzing sketch id3679_ultrasonido_control_sensor_car_new_0 (saved by Fritzing 0.9.2b)
circuit board: 14.5532cm x 7.30154cm
breadboards: 1

parts:
  IC1 = L293D [package=THT]
  M1 = DC Motor
  M2 = DC Motor
  Parte2 = HC-SR04 ultrasonic distance sensor
  VCC1 = Battery
  R1 = Resistor [tolerance=±5% resistance=220 package=THT]
  LED1 = LED - 5mm [color="Red (633nm)" package="5 mm [THT]"]
  Parte1 = Arduino Uno (Rev3)

nets (from the schematic view):
  N1: IC1.Enable_1, IC1.+V, Parte2.connector0, Parte1.5V
  N2: IC1.In_1, Parte1.D10_PWM/SS
  N3: IC1.Out_1_(_Controlled_by_Enable_1_), M1.pin_2
  N4: IC1.0V, VCC1.connector0
  N5: IC1.Out_2_(_Controlled_by_Enable_1_), M1.pin_1
  N6: IC1.In_2, Parte1.D9_PWM
  N7: IC1.+Vmotor, VCC1.connector1
  N8: IC1.In_3, Parte1.D5_PWM
  N9: IC1.Out_3_(_Controlled_by_Enable_2_), M2.pin_2
  N10: IC1.Out_4_(_Controlled_by_Enable_2_), M2.pin_1
  N11: IC1.In_4, Parte1.D6_PWM
  N12: Parte2.connector1, Parte1.D3_PWM
  N13: Parte2.connector2, Parte1.D2
  N14: Parte2.connector3, LED1.cathode, Parte1.GND
  N15: R1.Pin_0, LED1.anode
  N16: R1.Pin_1, Parte1.D13/SCK
