# Fritzing sketch id367_ArdLP1_V0_0 (saved by Fritzing 0.8.7b)
breadboards: 1

parts:
  R1 = Resistor [tolerance=±5% resistance=220 package=THT]
  R2 = Resistor [tolerance=±5% resistance=220 package=THT]
  R3 = Resistor [tolerance=±5% resistance=220 package=THT]
  LED1 = LED - 5mm [color="Yellow (595nm)" package="5 mm [THT]"]
  LED3 = LED - 5mm [color="Green (555nm)" package="5 mm [THT]"]
  LED4 = LED - 5mm [color="Red (633nm)" package="5 mm [THT]"]
  Composant1 = Arduino Ethernet Shield (Rev3)
  R4 = Trimmer Potentiometer [maximum_resistance=10kΩ package=THT]
  Matrix_keypad1 = CMG

nets:
  N1: R1.Pin_0, Composant1.SPI/D12
  N2: R1.Pin_1, LED1.anode
  N3: R2.Pin_0, Composant1.ETH_CS
  N4: R2.Pin_1, LED3.anode
  N5: R3.Pin_0, Composant1.PWM_D11
  N6: R3.Pin_1, LED4.anode
  N7: LED1.cathode, LED3.cathode, LED4.cathode, Composant1.GND, R4.leg2
  N8: Composant1.D8, Matrix_keypad1.connector31
  N9: Composant1.PWM_D9, Matrix_keypad1.connector32
  N10: Composant1.A0, R4.wiper
  N11: Composant1.D2, Matrix_keypad1.connector25
  N12: Composant1.PWM_D3, Matrix_keypad1.connector26
  N13: Composant1.SDCS, Matrix_keypad1.connector27
  N14: Composant1.PWM_D5, Matrix_keypad1.connector28
  N15: Composant1.PWM_D6, Matrix_keypad1.connector29
  N16: Composant1.D7, Matrix_keypad1.connector30
  N17: Composant1.5V, R4.leg1

notes:
  ArdLP1 - V0
  Octobre 2014
  J. Courbon - MMI Le Puy
  Platine DFRobot
