# Fritzing sketch id3680_sensorDistancia_0 (saved by Fritzing 0.9.3b)
circuit board: 8.46667cm x 5.64444cm
breadboards: 1

parts:
  Componente1 = Arduino Uno (Rev3)
  LED1 = LED - 5mm [color="Green (565nm)" package="5 mm [THT]"]
  LED2 = LED - 5mm [color="Yellow (595nm)" package="5 mm [THT]"]
  LED3 = LED - 5mm [color="Red (633nm)" package="5 mm [THT]"]
  hc-sr1 = hc-sr04

nets:
  N1: Componente1.D11_PWM/MOSI, LED3.cathode
  N2: Componente1.D12/MISO, LED2.cathode
  N3: Componente1.D13/SCK, LED1.cathode
  GND: Componente1.GND, LED1.anode, LED2.anode, LED3.anode, hc-sr1.Trig, hc-sr1.Echo, hc-sr1.GND
  5V: Componente1.5V, hc-sr1.VCC
