# Fritzing sketch id3681_Sensore_di_distanza_0 (saved by Fritzing 0.9.2b)
breadboards: 1

parts:
  LCD1 = LCD screen
  LED1 = RGB LED (com. cathode, rgb) [package="5 mm [THT]"]
  J1 = Piezo Speaker
  R1 = Resistor [tolerance=±5% resistance=220 package="0805 [SMD]"]  # not connected
  R2 = Resistor [tolerance=±5% resistance=220 package="0805 [SMD]"]
  R3 = Resistor [tolerance=±5% resistance=220 package="0805 [SMD]"]
  R4 = Resistor [tolerance=±5% resistance=220 package="0805 [SMD]"]
  R5 = Trimmer Potentiometer [maximum_resistance=10kΩ package=THT]
  Componente1 = Arduino Uno (Rev3)
  Componente2 = SRF05 Ultrasonic Rangefinder

nets:
  N1: LCD1.VSS, LCD1.R/W, LCD1.LED-, J1.pin1, R5.leg2, Componente2.connector11
  VDD: LCD1.VDD, LED1.common_cathode, R4.Pin_0, R5.leg1, Componente1.5V, Componente2.connector8
  N2: LCD1.V0, R5.wiper
  N3: LCD1.RS, Componente1.D12/MISO
  N4: LCD1.E, Componente1.D11_PWM/MOSI
  N5: LCD1.DB4, Componente1.D5_PWM
  N6: LCD1.DB5, Componente1.D4
  N7: LCD1.DB6, Componente1.D3_PWM
  N8: LCD1.DB7, Componente1.D2
  N9: LCD1.LED+, R4.Pin_1
  N10: LED1.green_anode, R2.Pin_0
  N11: LED1.blue_anode, R3.Pin_0
  N12: J1.pin2, Componente1.D9_PWM
  N13: R2.Pin_1, Componente1.D10_PWM/SS
  N14: R3.Pin_1, Componente1.D13/SCK
  N15: Componente1.D8, Componente2.connector9
  N16: Componente1.D7, Componente2.connector10

notes:
  led Rgb Catodo comune
  by A.Oss
