# Fritzing sketch id3682_g_sensore.movimento.speaker_0 (saved by Fritzing 0.8.7b)
breadboards: 1

parts:
  Componente1 = Arduino Uno (Rev3)
  J1 = Piezo Speaker
  U1 = TOUCH [package=touch2]  # not connected

nets:
  N1: Componente1.GND, J1.pin1
  N2: Componente1.D3_PWM, J1.pin2

notes:
  <--è UN SENSORE DI MOVIMENTO SEN0018
  scusate la confusione è il mio primo progetto...
