# Fritzing sketch id3683_sketchsensori_0 (saved by Fritzing 0.9.3b)
breadboards: 1

parts:
  Componente1 = Arduino Uno (Rev3)
  Chirp!_Soil_Moisture_Sensor1 = Chirp! Soil Moisture Sensor v2.7.3
  Chirp!_Soil_Moisture_Sensor2 = Chirp! Soil Moisture Sensor v2.7.3

nets:
  N1: Componente1.A0, Chirp!_Soil_Moisture_Sensor1.pin_3
  N2: Componente1.A1, Chirp!_Soil_Moisture_Sensor2.pin_3
  N3: Componente1.5V, Chirp!_Soil_Moisture_Sensor1.Pin_1, Chirp!_Soil_Moisture_Sensor2.Pin_1
  N4: Componente1.GND, Chirp!_Soil_Moisture_Sensor1.pin_5, Chirp!_Soil_Moisture_Sensor2.pin_5
