# Fritzing sketch id3684_SensorPresion_0 (saved by Fritzing 0.9.3b)

parts:
  Componente1 = Arduino Uno (Rev3)
  R1 = Resistor [tolerance=±5% resistance=10k package=THT]
  U1 = CAPSENSE_PAD [package=capsense_pad]

nets:
  N1: Componente1.A0, R1.Pin_1, U1.RES
  N2: Componente1.5V, U1.RECEIVE
  N3: Componente1.GND, R1.Pin_0
