# Fritzing sketch id3686_Sensor_Ultrasonido_0 (saved by Fritzing 0.9.3b)
breadboards: 1

parts:
  Arduino1 = Arduino
  LED1 = LED - 5mm [color="Red (633nm)" package="5 mm [THT]"]
  LED2 = LED - 5mm [color="Orange (620nm)" package="5 mm [THT]"]
  LED3 = LED - 5mm [color="Green (555nm)" package="5 mm [THT]"]
  R1 = Resistor [tolerance=±5% resistance=220 package=THT]
  R2 = Resistor [tolerance=±5% resistance=220 package=THT]
  Componente1 = JeePlug experimenter's board
  R4 = Resistor [tolerance=±5% resistance=220 package=THT]

nets:
  N1: Arduino1.D13, LED3.anode, R4.Pin_0, R4.Pin_1
  N2: Arduino1.D12, LED2.anode, R2.Pin_0, R2.Pin_1
  N3: Arduino1.D11, LED1.anode, R1.Pin_0, R1.Pin_1
  N4: Arduino1.D7, Componente1.B3
  N5: Arduino1.D6, Componente1.B4
  N6: Arduino1.+5V, Componente1.B5
  N7: Arduino1.GND, LED1.cathode, LED2.cathode, LED3.cathode, Componente1.B2

notes:
  HC-SRO4
