# Fritzing sketch id3687_sentry_circuit_0 (saved by Fritzing 0.9.0b)
breadboards: 1

parts:
  부품1 = Arduino Uno (Rev3)
  U1 = XBee
  R1 = Resistor [package="2512 [SMD]"]
  LED1 = smd LED [color="Red (633nm)" package="0805 [SMD]"]

nets (from the schematic view):
  N1: 부품1.D0/RX, U1.pin2
  N2: 부품1.D1/TX, U1.pin3
  3V3: 부품1.3V3, U1.VCC
  GND: 부품1.GND, U1.GND
  N3: U1.pin6, R1.Pin_0
  N4: R1.Pin_1, LED1.anode
