# Fritzing sketch id3688_Untitled_Sketch_0 (saved by Fritzing 0.9.2b)
breadboards: 1

parts:
  Componente1 = Arduino Uno (Rev3)
  LED1 = RGB LED (com. cathode, rgb) [package="5 mm [THT]"]
  J1 = Basic Servo

nets:
  N1: Componente1.D9_PWM, J1.vcc
  N2: Componente1.D2, LED1.red_anode
  N3: Componente1.D3_PWM, LED1.blue_anode
  N4: Componente1.D4, LED1.green_anode
  N5: Componente1.5V, J1.pulse
  N6: LED1.common_cathode, J1.gnd
