# Fritzing sketch id3689_i%3Ao_0 (saved by Fritzing 0.9.2b)
breadboards: 1

parts:
  Part1 = Arduino Uno (Rev3) - ICSP
  LED1 = DUO LED RG [package="5 mm [THT]"]
  LED2 = smd LED [color="Red (660nm)" package="0603 [SMD]"]
  LED3 = smd LED [color="Red (633nm)" package="0603 [SMD]"]
  LED4 = smd LED [color="Green (555nm)" package="0603 [SMD]"]
  S1 = Pushbutton [package="[SMD]"]
  R1 = Resistor [tolerance=±5% resistance=220 package="0805 [SMD]"]
  R2 = Resistor [tolerance=±5% resistance=220 package="0805 [SMD]"]
  R3 = Resistor [tolerance=±5% resistance=220 package="0805 [SMD]"]
  R4 = Resistor [tolerance=±5% resistance=220 package="0805 [SMD]"]
  R5 = Resistor [tolerance=±5% resistance=220 package="0805 [SMD]"]
  Part2 = Thumb Joystick

nets:
  N1: Part1.A0, Part2.HORZ
  N2: Part1.A1, Part2.VERT
  N3: Part1.D9_PWM, R4.Pin_1
  N4: Part1.D13/SCK, R2.Pin_1
  GND: Part1.GND, LED1.red_anode, LED2.cathode, LED3.cathode, LED4.cathode, R3.Pin_1, Part2.GND
  N5: Part1.D2, S1.Pin_1, S1.Pin_2, R3.Pin_0
  N6: Part1.D5_PWM, R5.Pin_1
  N7: Part1.D6_PWM, R1.Pin_1
  5V: Part1.5V, S1.Pin_3, S1.Pin_4, Part2.VCC
  N8: LED1.common_cathode, R2.Pin_0
  N9: LED2.anode, R1.Pin_0
  N10: LED3.anode, R5.Pin_0
  N11: LED4.anode, R4.Pin_0
