# Fritzing sketch id3690_Serial_Cable_Adaptor_0 (saved by Fritzing 0.9.1b)
circuit board: 5.40369cm x 1.81836cm
breadboards: 1

parts:
  Q1 = PNP-Transistor [package="TO92 [THT]"]
  Q2 = NPN-Transistor [package="TO92 [THT]"]
  JP2 = Header 3 [package=1x03-1mm-ra]
  R1 = Resistor [tolerance=±5% resistance=47k package=THT]
  R3 = Resistor [tolerance=±5% resistance=47k package=THT]
  JP3 = Header 2 [package=springterminal-2.54mm-2]
  R4 = Resistor [tolerance=±5% resistance=47k package=THT]

nets:
  N1: Q1.E, JP2.1
  N2: Q1.B, R1.Pin_1
  N3: Q1.C, R3.Pin_0, R4.Pin_0
  GND: Q2.E, JP2.3, JP3.2, R4.Pin_1
  N4: Q2.B, R3.Pin_1
  N5: Q2.C, JP3.1
  N6: JP2.2, R1.Pin_0
