# Fritzing sketch id3693_LED_RGB_3_POT_0 (saved by Fritzing 0.9.1b)
breadboards: 1

parts:
  Parte1 = Arduino Uno (Rev3)
  U1 = POT [package=pot_alpha_rv16af-20]
  U2 = POT [package=pot_alpha_rv16af-20]
  U3 = POT [package=pot_alpha_rv16af-20]
  LED1 = RGB LED (com. cathode, rbg) [package="5 mm [THT]"]
  R1 = Resistor [tolerance=±5% resistance=330 package=THT]
  R2 = Resistor [tolerance=±5% resistance=330 package=THT]
  R3 = Resistor [tolerance=±5% resistance=330 package=THT]

nets:
  N1: Parte1.A0, U1.S
  N2: Parte1.A1, U2.S
  N3: Parte1.A2, U3.S
  N4: Parte1.D3_PWM, R1.Pin_1
  N5: Parte1.D5_PWM, R2.Pin_1
  N6: Parte1.D6_PWM, R3.Pin_1
  N7: Parte1.5V, U1.A, U2.A, U3.A
  N8: Parte1.GND, U1.E, U2.E, U3.E, LED1.common_cathode
  N9: LED1.red_anode, R3.Pin_0
  N10: LED1.blue_anode, R2.Pin_0
  N11: LED1.green_anode, R1.Pin_0
