# Fritzing sketch id3695_Serial_Display_0 (saved by Fritzing 0.9.3b)
circuit board: 7.2cm x 4.52608cm
breadboards: 1

parts:
  J1 = double row male pin header, 6 pins [form="♂ (male)"]
  R1 = Resistor [tolerance=±5% resistance=10k package="1206 [SMD]"]
  C2 = Ceramic Capacitor [capacitance=10nF package="1206 [SMD, multilayer]"]
  C4 = Ceramic Capacitor [capacitance=100nF package="1206 [SMD, multilayer]"]
  Q1 = NPN-Transistor [package="SOT-23 [SMD]"]
  R2 = Resistor [tolerance=±5% resistance=2.2k package="1206 [SMD]"]
  R3 = Resistor [tolerance=±5% resistance=220 package="1206 [SMD]"]
  LED1 = LED - 3mm [color="Red (633nm)" package="3 mm [THT]"]
  LED2 = LED - 3mm [color="Red (633nm)" package="3 mm [THT]"]
  R4 = Resistor [tolerance=±5% resistance=220 package="1206 [SMD]"]
  Q2 = NPN-Transistor [package="SOT-23 [SMD]"]
  R5 = Resistor [tolerance=±5% resistance=2.2k package="1206 [SMD]"]
  LED3 = LED - 3mm [color="Red (633nm)" package="3 mm [THT]"]
  R6 = Resistor [tolerance=±5% resistance=220 package="1206 [SMD]"]
  Q3 = NPN-Transistor [package="SOT-23 [SMD]"]
  R7 = Resistor [tolerance=±5% resistance=2.2k package="1206 [SMD]"]
  LED4 = LED - 3mm [color="Red (633nm)" package="3 mm [THT]"]
  R8 = Resistor [tolerance=±5% resistance=220 package="1206 [SMD]"]
  Q4 = NPN-Transistor [package="SOT-23 [SMD]"]
  R9 = Resistor [tolerance=±5% resistance=2.2k package="1206 [SMD]"]
  LED5 = LED - 3mm [color="Red (633nm)" package="3 mm [THT]"]
  R10 = Resistor [tolerance=±5% resistance=220 package="1206 [SMD]"]
  Q5 = NPN-Transistor [package="SOT-23 [SMD]"]
  R11 = Resistor [tolerance=±5% resistance=2.2k package="1206 [SMD]"]
  LED7 = LED - 3mm [color="Red (633nm)" package="3 mm [THT]"]
  LED10 = LED - 3mm [color="Red (633nm)" package="3 mm [THT]"]
  LED9 = LED - 3mm [color="Red (633nm)" package="3 mm [THT]"]
  LED8 = LED - 3mm [color="Red (633nm)" package="3 mm [THT]"]
  R12 = Resistor [tolerance=±5% resistance=220 package="1206 [SMD]"]
  R13 = Resistor [tolerance=±5% resistance=220 package="1206 [SMD]"]
  R14 = Resistor [tolerance=±5% resistance=220 package="1206 [SMD]"]
  R15 = Resistor [tolerance=±5% resistance=220 package="1206 [SMD]"]
  R16 = Resistor [tolerance=±5% resistance=220 package="1206 [SMD]"]
  Q9 = NPN-Transistor [package="SOT-23 [SMD]"]
  Q7 = NPN-Transistor [package="SOT-23 [SMD]"]
  Q10 = NPN-Transistor [package="SOT-23 [SMD]"]
  Q8 = NPN-Transistor [package="SOT-23 [SMD]"]
  Q6 = NPN-Transistor [package="SOT-23 [SMD]"]
  R17 = Resistor [tolerance=±5% resistance=2.2k package="1206 [SMD]"]
  R18 = Resistor [tolerance=±5% resistance=2.2k package="1206 [SMD]"]
  R19 = Resistor [tolerance=±5% resistance=2.2k package="1206 [SMD]"]
  R20 = Resistor [tolerance=±5% resistance=2.2k package="1206 [SMD]"]
  R21 = Resistor [tolerance=±5% resistance=2.2k package="1206 [SMD]"]
  S1 = Round Pushbutton
  R22 = Resistor [tolerance=±5% resistance=10k package="1206 [SMD]"]
  R23 = Resistor [tolerance=±5% resistance=10k package="1206 [SMD]"]
  J2 = double row male pin header, 4 pins [form="♂ (male)"]
  C1 = Ceramic Capacitor [capacitance=100nF package="1206 [SMD, multilayer]"]
  S2 = Round Pushbutton
  C3 = Ceramic Capacitor [capacitance=100nF package="1206 [SMD, multilayer]"]
  LED6 = LED - 3mm [color="Red (633nm)" package="3 mm [THT]"]
  IC1 = MICROCONTROLLER [package=dil28-3-zif_socket]

nets:
  MISO: J1.pin1, IC1.PB4(MISO)
  5V: J1.pin2, R1.Pin_1, C4.1, R3.Pin_1, R4.Pin_1, R6.Pin_1, R8.Pin_1, R10.Pin_1, R12.Pin_1, R13.Pin_1, R14.Pin_1, R15.Pin_1, R16.Pin_1, R22.Pin_1, R23.Pin_1, J2.pin1, C1.1, C3.1, IC1.VCC, IC1.AVCC
  SCK: J1.pin3, IC1.PB5(SCK)
  MOSI: J1.pin4, IC1.PB3(MOSI_OC2)
  nRST: J1.pin5, R1.Pin_0, C2.1, IC1.PC6(_RESET)
  GND: J1.pin6, C2.0, C4.0, Q1.2, Q2.2, Q3.2, Q4.2, Q5.2, Q9.2, Q7.2, Q10.2, Q8.2, Q6.2, S1.leg1, J2.pin4, C1.0, S2.leg1, C3.0, IC1.GND, IC1.AGND
  N1: Q1.0, R2.Pin_1
  N2: Q1.1, LED1.cathode
  LED_01: R2.Pin_0, IC1.PC4(ADC4_SDA)
  N3: R3.Pin_0, LED1.anode
  N4: LED2.cathode, Q2.1
  N5: LED2.anode, R4.Pin_0
  N6: Q2.0, R5.Pin_1
  LED_02: R5.Pin_0, IC1.PC2(ADC2)
  N7: LED3.cathode, Q3.1
  N8: LED3.anode, R6.Pin_0
  N9: Q3.0, R7.Pin_1
  LED_03: R7.Pin_0, IC1.PC1(ADC1)
  N10: LED4.cathode, Q4.1
  N11: LED4.anode, R8.Pin_0
  N12: Q4.0, R9.Pin_1
  LED_04: R9.Pin_0, IC1.PB2(SS_OC1B)
  N13: LED5.cathode, Q5.1
  N14: LED5.anode, R10.Pin_0
  N15: Q5.0, R11.Pin_1
  LED_05: R11.Pin_0, IC1.PB0(ICP)
  N16: LED7.cathode, Q7.1
  N17: LED7.anode, R15.Pin_0
  N18: LED10.cathode, Q10.1
  N19: LED10.anode, R16.Pin_0
  N20: LED9.cathode, Q9.1
  N21: LED9.anode, R14.Pin_0
  N22: LED8.cathode, Q8.1
  N23: LED8.anode, R12.Pin_0
  N24: R13.Pin_0, LED6.anode
  N25: Q9.0, R20.Pin_1
  N26: Q7.0, R19.Pin_1
  N27: Q10.0, R21.Pin_1
  N28: Q8.0, R18.Pin_1
  N29: Q6.0, R17.Pin_1
  N30: Q6.1, LED6.cathode
  LED_06: R17.Pin_0, IC1.PC5(ADC5_SCL)
  LED_08: R18.Pin_0, IC1.PC0(ADC0)
  LED_07: R19.Pin_0, IC1.PC3(ADC3)
  LED_09: R20.Pin_0, IC1.PB1(OC1A)
  LED_10: R21.Pin_0, IC1.PD7(AIN1)
  SW_1: S1.leg0, R22.Pin_0, IC1.PD5(T1)
  SW_2: R23.Pin_0, S2.leg0, IC1.PD6(AIN0)
  UART_RX: J2.pin2, IC1.PD0(RXD)
  UART_TX: J2.pin3, IC1.PD1(TXD)

notes:
  Serial Display - 1.0
  Programmation interface
  Serial interface
  Serial interface for display (10 LED) and 2 switchs, 1
  Serial Display, Serial interface for display (10 LED) and 2 switchs, 1
