# Fritzing sketch id3696_serialPrint_Button_0 (saved by Fritzing 0.9.3b)
breadboards: 1

parts:
  Parça1 = Arduino Uno (Rev3) - ICSP
  S1 = Pushbutton [package="[THT]"]
  R1 = Resistor [tolerance=±5% resistance=220 package="2512 [SMD]"]

nets:
  N1: Parça1.D10_PWM/SS, S1.Pin_1, S1.Pin_2, R1.Pin_0
  N2: Parça1.5V, S1.Pin_3, S1.Pin_4
  N3: Parça1.GND, R1.Pin_1
