# Fritzing sketch id3699_serialduino_328_v1_0 (saved by Fritzing 0.9.0b)
circuit board: 6.858cm x 5.334cm
breadboards: 4

parts:
  Analog_Pins = FreeSensors-ArduinoAnalogPins [form="♀ (female)"]
  Power_Pins = FreeSensors-ArduinoPowerPins [form="♀ (female)"]
  DigiLow_Pins = FreeSensors-ArduinoDigiLowPins [form="♀ (female)"]
  DigiHigh_Pins = FreeSensors-ArduinoDigiHighPins [form="♀ (female)"]
  D1 = FreeSensors-1N5817 [part_number=1N5817]
  Power_plug = Power plug
  XTAL1 = Crystal [frequency="16 MHz" package=THT]
  RUN = LED - 3mm [color="Green (560nm)" package="3 mm [THT]"]
  RESET = Pushbutton [package="[THT]"]
  R4 = Resistor [tolerance=±5% resistance=1k package=THT]
  C1 = Ceramic Capacitor [capacitance=22pF package="100 mil [THT, multilayer]"]
  C2 = Ceramic Capacitor [capacitance=22pF package="100 mil [THT, multilayer]"]
  Power = LED - 3mm [color="Red (660nm)" package="3 mm [THT]"]
  R5 = Resistor [tolerance=±5% resistance=1k package=THT]
  C4 = Electrolytic Capacitor [capacitance=22µF voltage=16V package="100 mil [THT, electrolytic]"]
  C5 = Ceramic Capacitor [capacitance=100nF package="100 mil [THT, multilayer]"]
  R3 = Resistor [tolerance=±20% resistance=10k package=THT]
  U1 = Voltage Regulator - 5V [part_number=7805 package="TO220 [THT]"]
  C6 = Electrolytic Capacitor [capacitance=1µF voltage=16V package="100 mil [THT, electrolytic]"]
  ATmega328 = FreeSensors-ATmega328 [part_number=ATmega328]
  RXTX = FreeSensors-6P6Cjack [part_number=6P6C]
  C8 = Ceramic Capacitor [capacitance=100nF package="100 mil [THT, multilayer]"]
  JINT = male pin header, 2 pins [form="♂ (male)"]
  J5V = male pin header, 3 pins [form="♂ (male)"]
  C9 = Ceramic Capacitor [capacitance=100nF package="100 mil [THT, multilayer]"]
  JTTL = FreeSensors-SerialTTLpins [form="♂ (male)"]

nets:
  N1: Analog_Pins.connector0, ATmega328.connector22
  N2: Analog_Pins.connector1, ATmega328.connector23
  N3: Analog_Pins.connector2, ATmega328.connector24
  N4: Analog_Pins.connector3, ATmega328.connector25
  SDA: Analog_Pins.connector4, DigiHigh_Pins.connector8, ATmega328.connector26
  SCL: Analog_Pins.connector5, DigiHigh_Pins.connector9, ATmega328.connector27
  VIN: Power_Pins.connector0, D1.connector0, C4.+, U1.input_voltage, C9.0
  GND: Power_Pins.connector1, Power_Pins.connector2, DigiHigh_Pins.connector6, Power_plug.GND, RESET.Pin_1, RESET.Pin_2, R4.Pin_1, C1.0, C2.0, R5.Pin_1, C4.-, C5.1, U1.GND, C6.-, ATmega328.connector7, ATmega328.connector21, RXTX.connector3, C9.1, JTTL.connector0
  5V: Power_Pins.connector3, Power.anode, C5.0, R3.Pin_1, C6.+, ATmega328.connector6, ATmega328.connector19, RXTX.connector2, J5V.pin2
  Reset: Power_Pins.connector5, RESET.Pin_3, RESET.Pin_4, R3.Pin_0, ATmega328.connector0, JINT.pin2
  RX: DigiLow_Pins.connector0, ATmega328.connector1, RXTX.connector4, JTTL.connector3
  TX: DigiLow_Pins.connector1, ATmega328.connector2, RXTX.connector5, JTTL.connector4
  P2: DigiLow_Pins.connector2, ATmega328.connector3
  P3: DigiLow_Pins.connector3, ATmega328.connector4
  P4: DigiLow_Pins.connector4, ATmega328.connector5
  P5: DigiLow_Pins.connector5, ATmega328.connector10
  P6: DigiLow_Pins.connector6, ATmega328.connector11
  P7: DigiLow_Pins.connector7, ATmega328.connector12
  P8: DigiHigh_Pins.connector0, ATmega328.connector13
  P9: DigiHigh_Pins.connector1, ATmega328.connector14
  P10: DigiHigh_Pins.connector2, ATmega328.connector15
  P11: DigiHigh_Pins.connector3, ATmega328.connector16
  P12: DigiHigh_Pins.connector4, ATmega328.connector17
  P13: DigiHigh_Pins.connector5, RUN.anode, ATmega328.connector18
  ARef: DigiHigh_Pins.connector7, ATmega328.connector20
  N5: D1.connector1, Power_plug.VCC
  N6: XTAL1.pin_0, C2.1, ATmega328.connector9
  N7: XTAL1.pin_1, C1.1, ATmega328.connector8
  N8: RUN.cathode, R4.Pin_0
  N9: Power.cathode, R5.Pin_0
  N10: U1.output_voltage, J5V.pin1
  DTR: RXTX.connector1, C8.0, JTTL.connector5
  N11: C8.1, JINT.pin1
  N12: J5V.pin3, JTTL.connector2

notes:
  FreeSensors
  Serialduino
  v1
  DTR TX RX 5V   GND
  TTL Vin
