# Fritzing sketch id3702_Arduino_Servo_and_Lights_0 (saved by Fritzing 0.9.3b)
circuit board: 6.88458cm x 5.29463cm
stripboards: 1

parts:
  J4 = female pin header, 3 pins [form="♀ (female)"]
  LED1 = LED - 5mm [color="Red (633nm)" package="5 mm [THT]"]
  R1 = Resistor [tolerance=±5% resistance=220 package=THT]
  D1 = Diode [package=diode-1n4001]
  C1 = Electrolytic Capacitor [capacitance=10µF voltage=35V package="100 mil [THT, electrolytic]"]
  J6 = female pin header, 3 pins [form="♀ (female)"]
  J5 = female pin header, 3 pins [form="♀ (female)"]
  J7 = female pin header, 3 pins [form="♀ (female)"]
  J3 = Screw terminal - 2 pins [package=THT]
  R2 = Resistor [tolerance=±5% resistance=220 package=THT]
  R3 = Resistor [tolerance=±5% resistance=220 package=THT]
  R4 = Resistor [tolerance=±5% resistance=220 package=THT]
  Part1 = Arduino Uno (Rev3)

nets:
  N1: J4.pin1, LED1.anode, D1.C, C1.+, J6.pin1, J5.pin1, J3.pin1, Part1.5V
  N2: J4.pin2, R2.Pin_1
  N3: J4.pin3, R1.Pin_1, D1.A, C1.-, J6.pin3, J5.pin3, J7.pin3, J3.pin2, Part1.GND
  N4: LED1.cathode, R1.Pin_0
  N5: J6.pin2, R4.Pin_1
  N6: J5.pin2, R3.Pin_1
  N7: J7.pin2, Part1.D11_PWM/MOSI
  N8: R2.Pin_0, Part1.D3_PWM
  N9: R3.Pin_0, Part1.D5_PWM
  N10: R4.Pin_0, Part1.D6_PWM

notes:
  Servo 1
  Servo 2
  Servo 3
  LED
  Connect LED Supply here
  LED Supply voltage
