# Fritzing sketch id3704_pictorial_for_aurduino_&_servo_0 (saved by Fritzing 0.9.3b)
breadboards: 1

parts:
  Part1 = Arduino Nano (Rev3.0)
  J1 = Basic Servo
  LED1 = LED - 5mm [color="Red (633nm)" package="5 mm [THT]"]
  S1 = Toggle Switch [package=THT]
  S2 = Toggle Switch [package=THT]

nets:
  GND: Part1.GND, J1.gnd, LED1.cathode, S1.L1, S2.L1
  N1: Part1.D2, S1.COM
  N2: Part1.D3, S2.COM
  N3: Part1.D9, LED1.anode
  5V: Part1.5V, J1.vcc
  N4: Part1.D13/SCK, J1.pulse

notes:
  Positive 5 VDC
  Negative supply
  Top of travel Limit switch
  Bottom of travel Limit switch
  Positive 12 VDC
  to selector switch #1 - other side to negative
  to selector switch #2 - other side to negative
