# Fritzing sketch id3705_Servo_Control_0 (saved by Fritzing 0.9.2b)
breadboards: 1

parts:
  Part1 = Arduino Uno (Rev3)
  J1 = Basic Servo
  R1 = TRIMPOT [package=trimpot-5mm]
  C1 = Electrolytic Capacitor [capacitance=100µF package="200 mil [THT, electrolytic]"]
  C2 = Electrolytic Capacitor [capacitance=100µF package="200 mil [THT, electrolytic]"]

nets:
  N1: Part1.D9_PWM, J1.pulse
  5V: Part1.5V, J1.vcc, R1.WIPER, C1.+, C2.+
  GND: Part1.GND, J1.gnd, R1.CCW, C1.-, C2.-
