# Fritzing sketch id3706_ServoSkecth_0 (saved by Fritzing 0.7.12b)
breadboards: 1

parts:
  Arduino1 = Arduino
  J1 = female pin header, 6 pins [form="♀ (female)"]
  R1 = Trimmer Potentiometer [maximum_resistance=10kΩ package=THT]
  R2 = Photocell (LDR) [package=THT]
  R3 = Resistor [tolerance=±5% resistance=10k package=THT]
  J2 = male pin header, 3 pins [form="♂ (male)"]
  J3 = male pin header, 3 pins [form="♂ (male)"]
  J4 = female pin header, 2 pins [form="♀ (female)"]  # not connected
  J5 = Basic Servo
  J6 = Basic Servo

nets:
  VCC: Arduino1.+5V, R1.leg1, R3.Pin_1, J2.pin2, J3.pin2, J5.vcc, J6.vcc
  GND: Arduino1.GND, R1.leg2, R2.pin_0, J2.pin3, J3.pin3, J5.gnd, J6.gnd
  N1: Arduino1.A0, J1.pin1, R1.wiper
  N2: Arduino1.A1, J1.pin2, R2.pin_1, R3.Pin_0
  N3: Arduino1.A4, J1.pin5, J2.pin1, J5.pulse
  N4: Arduino1.A5, J1.pin6, J3.pin1, J6.pulse
