# Fritzing sketch id3707_FX5XQ1AHYH37YVU_0 (saved by Fritzing 0.8.3b)

parts:
  Part1 = Arduino Mega 2560 (Rev3)
  U1 = POT [package=pot_mammoth]
  M1 = DC Motor
  U2 = L298 [package=multiwatt15]
  U3 = LIPO-2000mAh [package=lipo-2000]

nets:
  N1: Part1.A2, U1.A
  N2: Part1.5V, U1.S
  N3: Part1.GND, U1.E, U3.-
  N4: Part1.D4_PWM, U2.ENA
  N5: Part1.D42, U2.IN1
  N6: Part1.D43, U2.IN2
  N7: M1.pin_1, U2.OUT2
  N8: M1.pin_2, U2.OUT1
  N9: U2.VS, U3.+

notes:
  physical connection here
