# Fritzing sketch id3708_Servo_Led_for_Skull_0 (saved by Fritzing 0.9.3b)
breadboards: 1

parts:
  Part1 = Arduino Uno (Rev3) - ICSP
  J1 = Basic Servo
  Part2 = Breakout Board for Electret Microphone
  R1 = Resistor [tolerance=±5% resistance=220 package="1206 [SMD]"]
  R2 = Resistor [tolerance=±5% resistance=220 package="1206 [SMD]"]
  LED1 = smd LED [color="Red (633nm)" package="0603 [SMD]"]
  LED2 = smd LED [color="Red (633nm)" package="0603 [SMD]"]

nets:
  N1: Part1.A0, Part2.VCC
  N2: Part1.D9_PWM, J1.pulse
  N3: Part1.D2, Part2.AUD
  N4: Part1.D3_PWM, R1.Pin_0, R2.Pin_0
  5V: Part1.5V, J1.vcc
  GND: Part1.GND, J1.gnd, Part2.GND, LED1.cathode, LED2.cathode
  N5: R1.Pin_1, R2.Pin_1, LED1.anode, LED2.anode

notes:
  The sound sensor is different, it has 4 pins, but didn't find it on the parts.
