# Fritzing sketch id3709_servo_test_0 (saved by Fritzing 0.9.0b)
breadboards: 1

parts:
  Part1 = Arduino Uno (Rev3) - ICSP
  J1 = Basic Servo
  BAT1 = Battery Holders [package=battery-aa-kit]
  BAT2 = Battery Holders [package=battery-aa-kit]  # not connected
  BAT3 = Battery Holders [package=battery-aa-kit]

nets:
  N1: Part1.D9_PWM, J1.pulse
  GND: Part1.GND, J1.gnd, BAT3.+
  N2: J1.vcc, BAT1.-
