# Fritzing sketch id3710_servomotor_0 (saved by Fritzing 0.9.2b)

parts:
  J1 = Basic Servo
  Parte1 = Arduino Uno (Rev3)

nets:
  GND: J1.gnd, Parte1.GND
  VCC: J1.vcc, Parte1.5V
  N1: J1.pulse, Parte1.D9_PWM
