# Fritzing sketch id3711_21_Servo_Motor_Control_Fritzing_0 (saved by Fritzing 0.8.7b)

parts:
  Part1 = Arduino Uno (Rev3)
  J1 = Basic Servo

nets:
  N1: Part1.D9_PWM, J1.pulse
  GND: Part1.GND, J1.gnd
  5V: Part1.5V, J1.vcc
