# Fritzing sketch id3713_ServoMotor_proj_0 (saved by Fritzing 0.9.2b)
breadboards: 1

parts:
  Part1 = Arduino Uno (Rev3)
  C1 = Electrolytic Capacitor [capacitance=100µF voltage=35V package="100 mil [THT, electrolytic]"]
  C2 = Electrolytic Capacitor [capacitance=100µF voltage=35V package="100 mil [THT, electrolytic]"]
  R1 = Rotary Potentiometer (Small) [maximum_resistance=100kΩ package=THT]
  J1 = Basic Servo

nets:
  N1: Part1.A0, R1.wiper
  N2: Part1.D9_PWM, J1.pulse
  5V: Part1.5V, C1.+, C2.+, R1.leg2, J1.vcc
  GND: Part1.GND, C1.-, C2.-, R1.leg1, J1.gnd
