# Fritzing sketch id3714_Servo_Motor_Set_Up_0 (saved by Fritzing 0.9.2b)
breadboards: 1

parts:
  Part1 = Arduino Uno (Rev3)
  J1 = Basic Servo
  C1 = Capacitor Polarized [package=panasonic_h13]
  C2 = Capacitor Polarized [package=panasonic_h13]
  U1 = POT [package=pot_mammoth]

nets:
  N1: Part1.A0, U1.A
  N2: Part1.D9_PWM, J1.pulse
  N3: J1.gnd, C2.-
  N4: J1.vcc, C2.+
  N5: C1.+, U1.E
  N6: C1.-, U1.S
