# Fritzing sketch id3715_nickwood_0 (saved by Fritzing 0.9.2b)
breadboards: 1

parts:
  Part1 = Arduino Uno (Rev3)
  J1 = Basic Servo
  C1 = Capacitor Polarized [package=panasonic_c]
  C2 = Capacitor Polarized [package=panasonic_c]
  R2 = Rotary Potentiometer (Small) [maximum_resistance=100kΩ package=THT]  # not connected

nets:
  5V: Part1.A0, Part1.5V, J1.vcc, C1.-, C2.+
  GND: Part1.GND, J1.gnd, C2.-
  N1: J1.pulse, C1.+
