# Fritzing sketch id3717_servomoteur_potentiometre_0 (saved by Fritzing 0.8.5b)
breadboards: 1

parts:
  R1 = Rotary Potentiometer (Small) [maximum_resistance=100kΩ package=THT]
  Composants1 = Arduino Uno (Rev3)
  J1 = Basic Servo

nets:
  GND: R1.leg1, Composants1.GND, J1.gnd
  N1: R1.wiper, Composants1.A1
  5V: R1.leg2, Composants1.5V, J1.vcc
  N2: Composants1.D5_PWM, J1.pulse
