# Fritzing sketch id371_Arduino_Safety_0 (saved by Fritzing 0.9.3b)
breadboards: 1

parts:
  R1 = Resistor [tolerance=±5% resistance=100 package=THT]
  J1 = Screw terminal - 2 pins [package=THT]
  R2 = Resistor [tolerance=±5% resistance=10k package=THT]
  J2 = Screw terminal - 2 pins [package=THT]
  R3 = Resistor [tolerance=±5% resistance=100 package=THT]
  R4 = Resistor [tolerance=±5% resistance=10k package=THT]
  J3 = Screw terminal - 2 pins [package=THT]
  J4 = Screw terminal - 2 pins [package=THT]
  R5 = Resistor [tolerance=±5% resistance=100 package=THT]
  R6 = Resistor [tolerance=±5% resistance=10k package=THT]
  J5 = Screw terminal - 2 pins [package=THT]
  J6 = Screw terminal - 2 pins [package=THT]
  R7 = Resistor [tolerance=±5% resistance=100 package=THT]
  R8 = Resistor [tolerance=±5% resistance=10k package=THT]
  J7 = Screw terminal - 2 pins [package=THT]
  R9 = Resistor [tolerance=±5% resistance=100 package=THT]
  R10 = Resistor [tolerance=±5% resistance=10k package=THT]
  J8 = Screw terminal - 2 pins [package=THT]
  J9 = Screw terminal - 2 pins [package=THT]
  R11 = Resistor [tolerance=±5% resistance=100 package=THT]
  R12 = Resistor [tolerance=±5% resistance=10k package=THT]
  R13 = Resistor [tolerance=±5% resistance=100 package=THT]
  R14 = Resistor [tolerance=±5% resistance=10k package=THT]
  J10 = Screw terminal - 2 pins [package=THT]
  J11 = Screw terminal - 2 pins [package=THT]
  J12 = Screw terminal - 2 pins [package=THT]
  J13 = Screw terminal - 2 pins [package=THT]
  J14 = Screw terminal - 2 pins [package=THT]
  R15 = Resistor [tolerance=±5% resistance=100 package=THT]
  R16 = Resistor [tolerance=±5% resistance=10k package=THT]
  J15 = Screw terminal - 2 pins [package=THT]
  J16 = Screw terminal - 2 pins [package=THT]
  J17 = Screw terminal - 2 pins [package=THT]
  R17 = Resistor [tolerance=±5% resistance=100 package=THT]
  R18 = Resistor [tolerance=±5% resistance=10k package=THT]
  J18 = Screw terminal - 2 pins [package=THT]
  J19 = Screw terminal - 2 pins [package=THT]
  R19 = Resistor [tolerance=±5% resistance=100 package=THT]
  J20 = Screw terminal - 2 pins [package=THT]
  R20 = Resistor [tolerance=±5% resistance=10k package=THT]
  J21 = Screw terminal - 2 pins [package=THT]

nets:
  N1: R1.Pin_0, J1.pin1
  N2: R1.Pin_1, R2.Pin_1, J2.pin1
  N3: R2.Pin_0, R4.Pin_0, R6.Pin_0, R8.Pin_0, R10.Pin_0, R12.Pin_0, R14.Pin_0, R16.Pin_0, J15.pin1, J15.pin2, R18.Pin_0, R20.Pin_0
  N4: R3.Pin_0, J3.pin1
  N5: R3.Pin_1, R4.Pin_1, J4.pin1
  N6: R5.Pin_0, J6.pin1
  N7: R5.Pin_1, R6.Pin_1, J5.pin1
  N8: R7.Pin_0, J11.pin1
  N9: R7.Pin_1, R8.Pin_1, J7.pin1
  N10: R9.Pin_0, J8.pin1
  N11: R9.Pin_1, R10.Pin_1, J9.pin1
  N12: R11.Pin_0, J13.pin1
  N13: R11.Pin_1, R12.Pin_1, J12.pin1
  N14: R13.Pin_0, J10.pin1
  N15: R13.Pin_1, J14.pin1
  N16: R15.Pin_0, J16.pin1
  N17: R15.Pin_1, R16.Pin_1, J17.pin1
  N18: R17.Pin_0, J19.pin1
  N19: R17.Pin_1, R18.Pin_1, J18.pin1
  N20: R19.Pin_0, J20.pin1
  N21: R19.Pin_1, R20.Pin_1, J21.pin1
