# Fritzing sketch id3720_ServoNOW_Shield_0 (saved by Fritzing 0.7.1b)

parts:
  J2 = Screw terminal - 2 pins [package=THT]
  Part3 = DB25M
  LED1 = LED - 5mm [color="Green (570nm)" package="5 mm [THT]"]
  R1 = Resistor [tolerance=±5% resistance=220 package=THT]
  R3 = Resistor [tolerance=±5% resistance=470 package=THT]
  R4 = Resistor [tolerance=±5% resistance=1k package=THT]
  J1 = Screw terminal - 2 pins [package=THT]
  Part2 = Arduino Prototyping Shield

nets:
  N1: J2.pin1, Part3.pin1, R1.Pin_1, Part2.N$35, Part2.N$67, Part2.N$74, Part2.N$84, Part2.N$90
  N2: J2.pin2, Part3.pin5, Part3.pin8, Part3.pin11, Part3.pin14, Part3.pin16, Part3.pin19, Part3.pin22, Part3.pin25, R3.Pin_1, R4.Pin_1, Part2.GND, Part2.N$30
  N3: Part3.pin2, J1.pin1, Part2.N$329
  N4: Part3.pin3, Part2.A1
  N5: Part3.pin4, Part2.AREF
  N6: Part3.pin6, Part2.D10
  N7: Part3.pin7, Part2.D11
  N8: Part3.pin9, Part2.D2
  N9: Part3.pin10, Part2.D3
  N10: Part3.pin12, Part2.D6
  N11: Part3.pin13, Part2.D7
  N12: Part3.pin15, J1.pin2, Part2.N$40
  N13: Part3.pin17, Part2.D8
  N14: Part3.pin18, Part2.D9
  N15: Part3.pin20, Part2.D12
  N16: Part3.pin21, Part2.D13
  N17: Part3.pin23, Part2.D4
  N18: Part3.pin24, Part2.D5
  N19: LED1.cathode, R3.Pin_0, Part2.N$54, Part2.N$55
  N20: LED1.anode, R1.Pin_0, R4.Pin_0, Part2.A0, Part2.N$65, Part2.N$66, Part2.N$78, Part2.N$79
