# Fritzing sketch id3722_7_seg_w_Arduino_0 (saved by Fritzing 0.7.10b)
breadboards: 1

parts:
  R1 = Resistor [tolerance=±5% resistance=220 package=THT]
  R2 = Resistor [tolerance=±5% resistance=220 package=THT]
  R3 = Resistor [tolerance=±5% resistance=220 package=THT]
  R4 = Resistor [tolerance=±5% resistance=220 package=THT]
  R5 = Resistor [tolerance=±5% resistance=220 package=THT]
  R6 = Resistor [tolerance=±5% resistance=220 package=THT]
  R7 = Resistor [tolerance=±5% resistance=220 package=THT]
  Arduino1 = Arduino
  7_Segment1 = 7 Segment Display

nets:
  N1: R1.Pin_0, Arduino1.D13
  N2: R1.Pin_1, 7_Segment1.Segment_B
  N3: R2.Pin_0, Arduino1.D12
  N4: R3.Pin_0, 7_Segment1.Segment_DP
  N5: R3.Pin_1, Arduino1.D11
  N6: R4.Pin_1, Arduino1.D9
  N7: R5.Pin_0, 7_Segment1.Segment_E, 7_Segment1.Segment_D
  N8: R5.Pin_1, Arduino1.D10
  N9: R6.Pin_0, Arduino1.D8
  N10: R6.Pin_1, 7_Segment1.Segment_F, 7_Segment1.Segment_G
  N11: R7.Pin_0, Arduino1.D7

notes:
  Controlling a 7 segment display with Arduino Uno
  <==USB Connector
  7 Segment Display
  common Cathode
