# Fritzing sketch id3723_seven_segment_0 (saved by Fritzing 0.8.7b)
breadboards: 1

parts:
  U1 = SPARKCORE
  JACK1 = 2.1mm_DC_Barrel_Jack
  R1 = Resistor [tolerance=±5% resistance=470 package=THT]
  R2 = Resistor [tolerance=±5% resistance=470 package=THT]
  7SEG1 = sevenseg
  7SEG2 = sevenseg

nets:
  N1: U1.connector51, JACK1.connector2, 7SEG1.connector3, 7SEG2.connector3
  N2: U1.connector52, JACK1.connector1, 7SEG1.connector2, 7SEG2.connector2
  N3: U1.connector53, R1.Pin_0, 7SEG1.connector4, 7SEG2.connector4
  N4: U1.connector54, R2.Pin_0, 7SEG1.connector5, 7SEG2.connector5
  N5: U1.connector64, R1.Pin_1, R2.Pin_1, 7SEG1.connector1, 7SEG2.connector1
