# Fritzing sketch id3724_ShakeMeLampe_0 (saved by Fritzing 0.8.5b)
circuit board: 5.11698cm x 5.50528cm
breadboards: 1

parts:
  U1 = Battery Holders [package=battery-aa-kit]
  S1 = Tilt Switch [package=THT]
  R1 = Resistor [tolerance=±5% resistance=220 package=THT]
  LED1 = LED - 5mm [color="White (6500K)" package="5 mm [THT]"]
  LED2 = LED - 5mm [color="White (8000K)" package="5 mm [THT]"]
  R2 = Resistor [tolerance=±5% resistance=220 package=THT]
  R3 = Resistor [tolerance=±5% resistance=220 package=THT]
  Bauteil1 = Arduino Leonardo (Rev3b)

nets:
  N1: U1.+, R1.Pin_0, Bauteil1.GND
  N2: U1.-, Bauteil1.VIN
  N3: S1.Pin_1, R1.Pin_1, Bauteil1.D3_PWM/SCL
  N4: S1.Pin_2, R2.Pin_0, Bauteil1.5V
  N5: LED1.cathode, LED2.cathode, R3.Pin_1
  N6: LED1.anode, Bauteil1.D9_PWM/A9
  N7: LED2.anode, Bauteil1.D8/A8
  N8: R2.Pin_1, R3.Pin_0
