# Fritzing sketch id3725_shapespeare_scanner_0 (saved by Fritzing 0.9.2b)

parts:
  Part2 = EasyDriver_v44
  LED1 = LEDs [package=led10mm]
  Part3 = Arduino Mega 2560 (Rev3)
  R1 = Resistor [tolerance=±5% resistance=220 package=THT]
  M1 = Stepper Motor - Bipolar  # not connected

nets:
  GND: Part2.GND, Part3.GND, R1.Pin_0
  N1: Part2.V+, Part3.VIN
  N2: Part2.STEP, Part3.D20/SDA
  N3: Part2.DIR, Part3.D21/SCL
  N4: Part2.ENABLE, Part3.D19/RX1
  N5: LED1.A, Part3.D53
