# Fritzing sketch id3726_switch_led_0 (saved by Fritzing 0.7.11b)
breadboards: 1

parts:
  Arduino1 = Arduino
  R1 = Resistor [tolerance=±5% resistance=220 package=THT]
  S1 = Toggle Switch [package=THT]
  LED1 = LED - 5mm [color="Red (633nm)" package="5 mm [THT]"]
  LED2 = LED - 5mm [color="Red (633nm)" package="5 mm [THT]"]

nets:
  N1: Arduino1.GND, LED1.cathode, LED2.anode
  N2: Arduino1.3V3, R1.Pin_0
  N3: R1.Pin_1, S1.COM
  N4: S1.L1, LED1.anode
  N5: S1.L2, LED2.cathode
