# Fritzing sketch id3727_Sharp_2Y0A21_0 (saved by Fritzing 0.9.2b)
breadboards: 1

parts:
  J1 = Infrared Proximity Sensor
  Parte1 = Arduino Uno (Rev3)

nets:
  N1: J1.Vout, Parte1.A0
  GND: J1.GND, Parte1.GND
  VCC: J1.Vcc, Parte1.5V
