# Fritzing sketch id3728_sharpiOS_0 (saved by Fritzing 0.7.5b)
breadboards: 1

parts:
  Arduino1 = Arduino
  TRRS1 = Audio Jack (TRRS) 3.5mm [part_number="LUMBERG JEITA RC-5325A" package="RC-5325A [SMD]"]
  R1 = Resistor [tolerance=±5% resistance=2k package=THT]
  C1 = Ceramic Capacitor [capacitance=2µF package="100 mil [THT, multilayer]"]
  R2 = Resistor [tolerance=±5% resistance=2k package=THT]
  R3 = Resistor [tolerance=±5% resistance=10k package=THT]
  J1 = Infrared Proximity Sensor

nets:
  GND: Arduino1.GND, TRRS1.RING2, R1.Pin_1, R2.Pin_1, J1.GND
  N1: Arduino1.D6, R3.Pin_0
  5V: Arduino1.VIN, J1.Vcc
  N2: Arduino1.A0, J1.Vout
  N3: TRRS1.SLEEVE, R1.Pin_0, C1.1
  N4: C1.0, R2.Pin_0, R3.Pin_1
