# Fritzing sketch id3729_reloj_nuevov2_0 (saved by Fritzing 0.9.0b)
circuit board: 11.724cm x 6.95081cm
breadboards: 3

parts:
  JP2 = M16 [package=1x16_machine-pin-header_lock.004]
  Parte1 = Arduino Nano (Rev3.0)
  JP1 = M16 [package=1x16_machine-pin-header_lock.004]
  Tiny_RTC1 = tinyRTC
  LED2 = LED - 5mm [color="Red (633nm)" package="5 mm [THT]"]
  LED4 = LED - 5mm [color="Red (633nm)" package="5 mm [THT]"]
  LED3 = LED - 5mm [color="Red (633nm)" package="5 mm [THT]"]
  8 = LED - 5mm [color="Red (633nm)" package="5 mm [THT]"]
  LED8 = LED - 5mm [color="Red (633nm)" package="5 mm [THT]"]
  LED9 = LED - 5mm [color="Red (633nm)" package="5 mm [THT]"]
  LED10 = LED - 5mm [color="Red (633nm)" package="5 mm [THT]"]
  S1 = Pushbutton [package=THT]
  LED12 = LED - 5mm [color="Red (633nm)" package="5 mm [THT]"]
  LED13 = LED - 5mm [color="Red (633nm)" package="5 mm [THT]"]
  R2 = Resistor [tolerance=±5% resistance=220 package=THT]
  LED5 = LED - 5mm [color="Red (633nm)" package="5 mm [THT]"]
  LED6 = LED - 5mm [color="Red (633nm)" package="5 mm [THT]"]
  LED7 = LED - 5mm [color="Red (633nm)" package="5 mm [THT]"]
  JP3 = M16 [package=1x16_machine-pin-header_lock.004]
  JP4 = M16 [package=1x16_machine-pin-header_lock.004]
  R3 = Resistor [tolerance=±5% resistance=220 package=THT]
  R4 = Resistor [tolerance=±5% resistance=220 package=THT]
  R5 = Resistor [tolerance=±5% resistance=220 package=THT]
  R6 = Resistor [tolerance=±5% resistance=220 package=THT]
  R7 = Resistor [tolerance=±5% resistance=220 package=THT]
  R8 = Resistor [tolerance=±5% resistance=220 package=THT]
  R9 = Resistor [tolerance=±5% resistance=220 package=THT]
  R10 = Resistor [tolerance=±5% resistance=220 package=THT]
  R11 = Resistor [tolerance=±5% resistance=220 package=THT]
  R12 = Resistor [tolerance=±5% resistance=220 package=THT]
  R13 = Resistor [tolerance=±5% resistance=220 package=THT]

nets:
  N1: JP2.1, Parte1.D13/SCK, 8.anode, JP4.1
  N2: JP2.2, Parte1.3V3, JP4.2
  N3: JP2.3, Parte1.AREF, JP4.3
  N4: JP2.4, Parte1.A0, LED12.anode, JP4.4
  N5: JP2.5, Parte1.A1, JP4.5
  N6: JP2.6, Parte1.A2, JP4.6
  N7: JP2.8, Parte1.A4, Tiny_RTC1.connector8, JP4.8
  N8: JP2.9, Parte1.A5, JP4.9
  N9: JP2.10, Parte1.A6, JP4.10
  N10: JP2.11, Parte1.A7, JP4.11
  N11: JP2.12, Parte1.5V, Tiny_RTC1.connector9, JP4.12
  N12: JP2.13, Parte1.RESET, JP1.13, JP3.13, JP4.13
  N13: JP2.14, Parte1.GND, JP1.12, Tiny_RTC1.connector10, S1.leg1, R2.Pin_0, JP3.12, JP4.14, R3.Pin_0, R4.Pin_0, R5.Pin_0, R7.Pin_0, R8.Pin_0, R9.Pin_0, R10.Pin_0, R11.Pin_0, R12.Pin_0, R13.Pin_0
  N14: JP2.15, Parte1.VIN, JP4.15
  N15: JP2.16, JP4.16
  N16: Parte1.D1/TX, JP1.15, JP3.15
  N17: Parte1.D0/RX, JP1.14, JP3.14
  N18: Parte1.D2, JP1.11, S1.leg0, JP3.11
  N19: Parte1.D3, JP1.10, Tiny_RTC1.connector5, LED13.anode, JP3.10
  N20: Parte1.D4, JP1.9, LED10.anode, JP3.9
  N21: Parte1.D5, JP1.8, LED9.anode, JP3.8
  N22: Parte1.D6, JP1.7, LED8.anode, JP3.7
  N23: Parte1.D7, JP1.6, LED7.anode, JP3.6
  N24: Parte1.D8, JP1.5, LED6.anode, JP3.5
  N25: Parte1.D9, JP1.4, LED5.anode, JP3.4
  N26: Parte1.D10, JP1.3, LED4.anode, JP3.3
  N27: Parte1.D11/MOSI, JP1.2, LED3.anode, JP3.2
  N28: Parte1.D12/MISO, JP1.1, LED2.anode, JP3.1
  N29: Parte1.A3, JP4.7
  N30: JP1.16, JP3.16
  N31: LED2.cathode, R9.Pin_1
  N32: LED4.cathode, R7.Pin_1
  N33: LED3.cathode, R8.Pin_1
  N34: 8.cathode, R3.Pin_1
  N35: LED8.cathode, R10.Pin_1
  N36: LED9.cathode, R11.Pin_1
  N37: LED10.cathode, R12.Pin_1
  N38: LED12.cathode, R13.Pin_1
  N39: LED13.cathode, R2.Pin_1
  N40: LED5.cathode, R6.Pin_1
  N41: LED6.cathode, R5.Pin_1
  N42: LED7.cathode, R4.Pin_1

notes:
  8
  32
  1
  2
  4
  16
  • PM
  ◦ AM
  seg
  Config
  Reloj Shield
  para
  Arduino
  Esneyder Morcillo
  César Tejada
