# Fritzing sketch id372_Ardu_I_O_0 (saved by Fritzing 0.9.2b)
breadboards: 2

parts:
  U1 = 74HC595 [package="DIP16 [THT]"]
  Part1 = Arduino Uno (Rev3)
  LCD1 = LCD screen
  R1 = Resistor [tolerance=±5% resistance=220 package=THT]
  R2 = Resistor [tolerance=±5% resistance=220 package=THT]
  R3 = Resistor [tolerance=±5% resistance=220 package=THT]
  R4 = Resistor [tolerance=±5% resistance=220 package=THT]
  R5 = Resistor [tolerance=±5% resistance=220 package=THT]
  R6 = Resistor [tolerance=±5% resistance=220 package=THT]
  R7 = Resistor [tolerance=±5% resistance=220 package=THT]
  R8 = Resistor [tolerance=±5% resistance=220 package=THT]
  R9 = Resistor [tolerance=±5% resistance=220 package=THT]
  LED1 = LED - 5mm [color="Red (633nm)" package="5 mm [THT]"]
  LED2 = LED - 5mm [color="Red (633nm)" package="5 mm [THT]"]
  LED3 = LED - 5mm [color="Red (633nm)" package="5 mm [THT]"]
  LED4 = LED - 5mm [color="Red (633nm)" package="5 mm [THT]"]
  LED5 = LED - 5mm [color="Red (633nm)" package="5 mm [THT]"]
  LED6 = LED - 5mm [color="Red (633nm)" package="5 mm [THT]"]
  LED7 = LED - 5mm [color="Red (633nm)" package="5 mm [THT]"]
  LED8 = LED - 5mm [color="Red (633nm)" package="5 mm [THT]"]
  R10 = Resistor [tolerance=±5% resistance=220 package=THT]
  R11 = Resistor [tolerance=±5% resistance=220 package=THT]
  R12 = Resistor [tolerance=±5% resistance=220 package=THT]
  LED9 = RGB LED (com. cathode, rgb) [package="5 mm [THT]"]
  R13 = Trimmer Potentiometer [maximum_resistance=10kΩ package=THT]

nets:
  N1: U1.Q1, R1.Pin_0
  N2: U1.Q2, R2.Pin_0
  N3: U1.Q3, R3.Pin_0
  N4: U1.Q4, R5.Pin_0
  N5: U1.Q5, R6.Pin_0
  N6: U1.Q6, R7.Pin_0
  N7: U1.Q7, R8.Pin_0
  GND: U1.GND, U1.OE, Part1.GND, LCD1.V0, LCD1.LED-, LED1.cathode, LED2.cathode, LED3.cathode, LED4.cathode, LED5.cathode, LED6.cathode, LED7.cathode, LED8.cathode, LED9.common_cathode, R13.leg1
  VCC: U1.MR, U1.VCC, Part1.5V, R9.Pin_0, R13.leg2
  N8: U1.SH_CP, Part1.D4
  N9: U1.ST_CP, Part1.D3_PWM
  N10: U1.DS, Part1.D2
  N11: U1.Q0, R4.Pin_0
  N12: Part1.D8, LCD1.DB7
  N13: Part1.D9_PWM, R12.Pin_0
  N14: Part1.D10_PWM/SS, R11.Pin_0
  N15: Part1.D11_PWM/MOSI, R10.Pin_0
  N16: Part1.D12/MISO, LCD1.RS
  N17: Part1.D13/SCK, LCD1.VDD
  N18: Part1.D5_PWM, LCD1.DB4
  N19: Part1.D6_PWM, LCD1.DB5
  N20: Part1.D7, LCD1.DB6
  N21: LCD1.VSS, R13.wiper
  N22: LCD1.LED+, R9.Pin_1
  N23: R1.Pin_1, LED2.anode
  N24: R2.Pin_1, LED3.anode
  N25: R3.Pin_1, LED4.anode
  N26: R4.Pin_1, LED1.anode
  N27: R5.Pin_1, LED5.anode
  N28: R6.Pin_1, LED6.anode
  N29: R7.Pin_1, LED7.anode
  N30: R8.Pin_1, LED8.anode
  N31: R10.Pin_1, LED9.blue_anode
  N32: R11.Pin_1, LED9.green_anode
  N33: R12.Pin_1, LED9.red_anode
