# Fritzing sketch id3730_Shield_H_Bridge_0 (saved by Fritzing 0.9.0b)
circuit board: 6.42563cm x 5.62467cm
breadboards: 1

parts:
  L293D = H-Bridge [package=THT]
  J5 = screw terminal, 2 pins
  J6 = screw terminal, 2 pins
  ULN2003 = ULN2003A [package="DIP16 [THT]"]
  J7 = double row female pin header, 12 pins [form="♀ (female)"]
  Parte1 = Arduino Uno (Rev3)
  M1 = DC Motor  # not connected
  M2 = Stepper Motor - Bipolar  # not connected

nets:
  N1: L293D.1Y, J6.pin2
  GND1: L293D.GND1, L293D.GND2, L293D.GND3, L293D.GND4, ULN2003.0V, Parte1.GND
  N2: L293D.2Y, J6.pin1
  N3: L293D.2A, Parte1.D7
  N4: L293D.VCC2, ULN2003.COM_-_Common, J7.pin1, J7.pin2, J7.pin3, J7.pin4, J7.pin5, J7.pin6, Parte1.VIN
  N5: L293D.3_4EN, Parte1.D3_PWM
  N6: L293D.3A, Parte1.D2
  N7: L293D.3Y, J5.pin2
  N8: L293D.4Y, J5.pin1
  N9: L293D.4A, Parte1.D4
  N10: L293D.VCC1, Parte1.5V
  N11: ULN2003.In_1, Parte1.D8
  N12: ULN2003.In_2, Parte1.D9_PWM
  N13: ULN2003.In_3, Parte1.D10_PWM/SS
  N14: ULN2003.In_4, Parte1.D11_PWM/MOSI
  N15: ULN2003.In_5, Parte1.D12/MISO
  N16: ULN2003.In_6, Parte1.D13/SCK
  N17: ULN2003.Out_6, J7.pin12
  N18: ULN2003.Out_5, J7.pin11
  N19: ULN2003.Out_4, J7.pin10
  N20: ULN2003.Out_3, J7.pin9
  N21: ULN2003.Out_2, J7.pin8
  N22: ULN2003.Out_1, J7.pin7

notes:
  D2
  D4
  D3
  D5
  D6
  D7
