# Fritzing sketch id3731_shield7segment_0 (saved by Fritzing 0.9.2b)
circuit board: 6.90107cm x 5.32929cm
breadboards: 1

parts:
  Parte1 = Arduino Uno (Rev3) - ICSP
  7_Segment1 = 7 Segment Display

nets:
  N1: Parte1.D8, 7_Segment1.Segment_G
  N2: Parte1.D9_PWM, 7_Segment1.Segment_DP
  N3: Parte1.GND, 7_Segment1.common_anode
  N4: Parte1.D2, 7_Segment1.Segment_A
  N5: Parte1.D3_PWM, 7_Segment1.Segment_B
  N6: Parte1.D4, 7_Segment1.Segment_C
  N7: Parte1.D5_PWM, 7_Segment1.Segment_D
  N8: Parte1.D6_PWM, 7_Segment1.Segment_E
  N9: Parte1.D7, 7_Segment1.Segment_F
