# Fritzing sketch id3732_multiplexing_shiftregister_0 (saved by Fritzing 0.8.3b)
breadboards: 2

parts:
  U1 = 74HC595 [package="DIP16 [THT]"]
  Bauteil1 = Arduino Uno (Rev3)
  LED1 = LED - 5mm [color="Red (633nm)" package="5 mm [THT]"]
  R1 = Resistor [tolerance=±5% resistance=220 package=THT]
  LED2 = LED - 5mm [color="Red (633nm)" package="5 mm [THT]"]
  R2 = Resistor [tolerance=±5% resistance=220 package=THT]
  LED3 = LED - 5mm [color="Red (633nm)" package="5 mm [THT]"]
  R3 = Resistor [tolerance=±5% resistance=220 package=THT]
  LED4 = LED - 5mm [color="Red (633nm)" package="5 mm [THT]"]
  R4 = Resistor [tolerance=±5% resistance=220 package=THT]
  LED5 = LED - 5mm [color="Red (633nm)" package="5 mm [THT]"]
  R5 = Resistor [tolerance=±5% resistance=220 package=THT]
  LED6 = LED - 5mm [color="Red (633nm)" package="5 mm [THT]"]
  R6 = Resistor [tolerance=±5% resistance=220 package=THT]
  LED7 = LED - 5mm [color="Red (633nm)" package="5 mm [THT]"]
  R7 = Resistor [tolerance=±5% resistance=220 package=THT]
  LED8 = LED - 5mm [color="Red (633nm)" package="5 mm [THT]"]
  R8 = Resistor [tolerance=±5% resistance=220 package=THT]

nets:
  N1: U1.Q1, LED2.cathode, LED2.anode, R2.Pin_1
  N2: U1.Q2, LED3.cathode, LED3.anode, R3.Pin_1
  N3: U1.Q3, LED4.cathode, LED4.anode, R4.Pin_1
  N4: U1.Q4, LED5.cathode, LED5.anode, R5.Pin_1
  N5: U1.Q5, LED6.cathode, LED6.anode, R6.Pin_1
  N6: U1.Q6, LED7.cathode, LED7.anode, R7.Pin_1
  N7: U1.Q7, LED8.cathode, LED8.anode, R8.Pin_1
  GND: U1.GND, U1.OE, Bauteil1.GND, R1.Pin_0, R2.Pin_0, R3.Pin_0, R4.Pin_0, R5.Pin_0, R6.Pin_0, R7.Pin_0, R8.Pin_0
  VCC: U1.MR, U1.VCC, Bauteil1.5V
  N8: U1.SH_CP, Bauteil1.ICSP_MISO, Bauteil1.D12/MISO
  N9: U1.ST_CP, Bauteil1.D8
  N10: U1.DS, Bauteil1.ICSP_MOSI, Bauteil1.D11_PWM/MOSI
  N11: U1.Q0, LED1.cathode, LED1.anode, R1.Pin_1

notes:
  /**
  * Shift Register Example
  * for 74HC595 456shift register
  * http://arduino.cc/en/Tutorial/ShiftOut
  * This sketch turns 8 LEDs on and of based on bytes
  * send to a 74HC595 shift register.
  *
  * based on Tim Igoes Sketch one by one
  * http://arduino.cc/en/Tutorial/ShftOut12
  *
  * Hardware:
  * * 74HC595 shift register attached to pins 8, 11, and 12 of the Arduino
  * * LEDs attached to each of the outputs of the shift register
  *
  * by Fabian Moron Zirfas
  *
  */
  //Pin connected to latch pin (ST_CP) of 74HC595
  const int latchPin = 8;
  //Pin connected to clock pin (SH_CP) of 74HC595
  const int clockPin = 12;
  //Pin connected to Data in (DS) of 74HC595
  const int dataPin = 11;
  //this holds our pattern an array of arrays (matrix)
  char vals [8][8] = {
  {'0','1','2','3','4','5','6','0'},
  {'4','2','2','3','5','7','0','3'},
  {'0','5','4','0','2','2','3','6'},
  {'2','7','2','6','6','4','1','4'},
  {'7','4','5','5','6','3','0','3'},
  {'3','3','5','7','7','1','4','3'},
  {'6','2','7','1','0','6','4','2'},
  {'5','1','3','0','0','5','7','6'}
  };
  void setup() {
  //set pins to output because they are addressed in the main loop
  pinMode(latchPin, OUTPUT);
  pinMode(dataPin, OUTPUT);
  pinMode(clockPin, OUTPUT);
  }
  void loop() {
  for(int i = 0; i < 8;i++){
  for(int j=0; j< 8; j++){
  registerWrite(vals[i][j], HIGH);
  delay(100); // wait a moment
  }
  }
  }
  // This method sends bits to the shift register:
  void registerWrite(char pin, int whichState) {
  // ASCII '0' through '9' characters are
  // represented by the values 48 through 57.
  // so if the you send a number from 0 through 7 in ASCII,
  // you can subtract 48 to get the actual value:
  int bitToSet = pin - 48;
  // the bits you want to send
  byte bitsToSend = 0;
  // turn off the output so the pins don't light up
  // while you're shifting bits:
  digitalWrite(latchPin, LOW);
  // turn on the next highest bit in bitsToSend:
  bitWrite(bitsToSend, bitToSet, whichState);
  // shift the bits out:
  shiftOut(dataPin, clockPin, MSBFIRST, bitsToSend);
  // turn on the output so the LEDs can light up:
  digitalWrite(latchPin, HIGH);
  }
