# Fritzing sketch id3733_Shift_out_Board_6_registers_0 (saved by Fritzing 0.8.6b)
circuit board: 9.27861cm x 6.21784cm
breadboards: 1

parts:
  SR_1 = 74HC595 [package="DIP16 [THT]"]
  SR_2 = 74HC595 [package="DIP16 [THT]"]
  SR_3 = 74HC595 [package="DIP16 [THT]"]
  SR_6 = 74HC595 [package="DIP16 [THT]"]
  SR_5 = 74HC595 [package="DIP16 [THT]"]
  SR_4 = 74HC595 [package="DIP16 [THT]"]
  R1 = Resistor [tolerance=±5% resistance=220 package=THT]
  R2 = Resistor [tolerance=±5% resistance=220 package=THT]
  C1 = Tantalum Capacitor [capacitance=1μF package="100 mil [THT, tantalum]"]
  LED1 = LED - 5mm [color="Red (633nm)" package="5 mm [THT]"]
  LED2 = LED - 5mm [color="Red (633nm)" package="5 mm [THT]"]
  IR_-_S = Infrared Proximity Sensor
  R4 = Resistor [tolerance=±5% resistance=220 package=THT]
  R3 = Resistor [tolerance=±5% resistance=220 package=THT]
  R5 = Resistor [tolerance=±5% resistance=220 package=THT]
  R6 = Resistor [tolerance=±5% resistance=220 package=THT]
  R7 = Resistor [tolerance=±5% resistance=220 package=THT]
  R8 = Resistor [tolerance=±5% resistance=220 package=THT]
  R9 = Resistor [tolerance=±5% resistance=220 package=THT]
  R10 = Resistor [tolerance=±5% resistance=220 package=THT]
  R11 = Resistor [tolerance=±5% resistance=220 package=THT]
  R12 = Resistor [tolerance=±5% resistance=220 package=THT]
  R13 = Resistor [tolerance=±5% resistance=220 package=THT]
  R14 = Resistor [tolerance=±5% resistance=220 package=THT]
  R15 = Resistor [tolerance=±5% resistance=220 package=THT]
  R16 = Resistor [tolerance=±5% resistance=220 package=THT]
  R17 = Resistor [tolerance=±5% resistance=220 package=THT]
  R18 = Resistor [tolerance=±5% resistance=220 package=THT]
  R19 = Resistor [tolerance=±5% resistance=220 package=THT]
  R20 = Resistor [tolerance=±5% resistance=220 package=THT]
  R21 = Resistor [tolerance=±5% resistance=220 package=THT]
  R22 = Resistor [tolerance=±5% resistance=220 package=THT]
  R23 = Resistor [tolerance=±5% resistance=220 package=THT]
  R24 = Resistor [tolerance=±5% resistance=220 package=THT]
  R25 = Resistor [tolerance=±5% resistance=220 package=THT]
  R26 = Resistor [tolerance=±5% resistance=220 package=THT]
  R27 = Resistor [tolerance=±5% resistance=220 package=THT]
  R28 = Resistor [tolerance=±5% resistance=220 package=THT]
  R29 = Resistor [tolerance=±5% resistance=220 package=THT]
  R30 = Resistor [tolerance=±5% resistance=220 package=THT]
  R31 = Resistor [tolerance=±5% resistance=220 package=THT]
  R32 = Resistor [tolerance=±5% resistance=220 package=THT]
  R33 = Resistor [tolerance=±5% resistance=220 package=THT]
  R34 = Resistor [tolerance=±5% resistance=220 package=THT]
  R35 = Resistor [tolerance=±5% resistance=220 package=THT]
  R36 = Resistor [tolerance=±5% resistance=220 package=THT]
  R37 = Resistor [tolerance=±5% resistance=220 package=THT]
  R38 = Resistor [tolerance=±5% resistance=220 package=THT]
  R39 = Resistor [tolerance=±5% resistance=220 package=THT]
  R40 = Resistor [tolerance=±5% resistance=220 package=THT]
  R41 = Resistor [tolerance=±5% resistance=220 package=THT]
  R42 = Resistor [tolerance=±5% resistance=220 package=THT]
  R43 = Resistor [tolerance=±5% resistance=220 package=THT]
  R44 = Resistor [tolerance=±5% resistance=220 package=THT]
  J8 = female pin header, 8 pins [form="♀ (female)"]
  J7 = female pin header, 9 pins [form="♀ (female)"]
  R45 = Resistor [tolerance=±5% resistance=220 package=THT]
  J6 = female pin header, 9 pins [form="♀ (female)"]
  R46 = Resistor [tolerance=±5% resistance=220 package=THT]
  R47 = Resistor [tolerance=±5% resistance=220 package=THT]
  J9 = female pin header, 9 pins [form="♀ (female)"]
  J4 = female pin header, 9 pins [form="♀ (female)"]
  R48 = Resistor [tolerance=±5% resistance=220 package=THT]
  R49 = Resistor [tolerance=±5% resistance=220 package=THT]
  J3 = female pin header, 9 pins [form="♀ (female)"]
  J2 = female pin header, 9 pins [form="♀ (female)"]
  R50 = Resistor [tolerance=±5% resistance=220 package=THT]
  J10 = female pin header, 5 pins [form="♀ (female)"]
  Pad1 = Pad [width=2.07759732431687 height=2.25061255210756 connect=center]
  Pad2 = Pad [width=1.90379945001292 height=1.98991574065165 connect=center]
  R51 = Resistor [tolerance=±5% resistance=220 package=THT]

nets:
  N1: SR_1.Q1, R10.Pin_1
  N2: SR_1.Q2, R14.Pin_1
  N3: SR_1.Q3, R13.Pin_1
  N4: SR_1.Q4, R12.Pin_1
  N5: SR_1.Q5, R16.Pin_1
  N6: SR_1.Q6, R15.Pin_1
  N7: SR_1.Q7, R11.Pin_1
  GND: SR_1.GND, SR_1.OE, SR_2.GND, SR_2.OE, SR_3.GND, SR_3.OE, SR_6.GND, SR_6.OE, SR_5.GND, SR_5.OE, SR_4.GND, SR_4.OE, R1.Pin_0, R2.Pin_0, C1.-, IR_-_S.GND, J8.pin3, J7.pin9, J6.pin9, J9.pin9, J4.pin1, J3.pin1, J2.pin1, J10.pin2, Pad2.pad
  N8: SR_1.Q7', SR_2.DS
  VCC: SR_1.MR, SR_1.VCC, SR_2.MR, SR_2.VCC, SR_3.MR, SR_3.VCC, SR_6.MR, SR_6.VCC, SR_5.MR, SR_5.VCC, SR_4.MR, SR_4.VCC, IR_-_S.Vcc, J8.pin2, J10.pin1, R51.Pin_0
  N9: SR_1.SH_CP, SR_2.SH_CP, SR_3.SH_CP, SR_6.SH_CP, SR_5.SH_CP, SR_4.SH_CP, J8.pin6, J10.pin5
  N10: SR_1.ST_CP, SR_2.ST_CP, SR_3.ST_CP, SR_6.ST_CP, SR_5.ST_CP, SR_4.ST_CP, C1.+, J8.pin5, J10.pin4
  N11: SR_1.DS, J8.pin4
  N12: SR_1.Q0, R45.Pin_1
  N13: SR_2.Q1, R42.Pin_1
  N14: SR_2.Q2, R43.Pin_1
  N15: SR_2.Q3, R21.Pin_1
  N16: SR_2.Q4, R20.Pin_1
  N17: SR_2.Q5, R19.Pin_1
  N18: SR_2.Q6, R18.Pin_1
  N19: SR_2.Q7, R17.Pin_1
  N20: SR_2.Q7', SR_3.DS
  N21: SR_2.Q0, R46.Pin_1
  N22: SR_3.Q1, R22.Pin_1
  N23: SR_3.Q2, R41.Pin_1
  N24: SR_3.Q3, R26.Pin_1
  N25: SR_3.Q4, R25.Pin_1
  N26: SR_3.Q5, R24.Pin_1
  N27: SR_3.Q6, R23.Pin_1
  N28: SR_3.Q7, R47.Pin_1
  N29: SR_3.Q7', SR_4.DS
  N30: SR_3.Q0, R27.Pin_1
  N31: SR_6.Q1, R9.Pin_0
  N32: SR_6.Q2, R8.Pin_0
  N33: SR_6.Q3, R7.Pin_0
  N34: SR_6.Q4, R6.Pin_0
  N35: SR_6.Q5, R5.Pin_0
  N36: SR_6.Q6, R4.Pin_0
  N37: SR_6.Q7, R50.Pin_0
  N38: SR_6.Q7', J10.pin3
  N39: SR_6.DS, SR_5.Q7'
  N40: SR_6.Q0, R3.Pin_0
  N41: SR_5.Q1, R28.Pin_0
  N42: SR_5.Q2, R44.Pin_0
  N43: SR_5.Q3, R29.Pin_0
  N44: SR_5.Q4, R30.Pin_0
  N45: SR_5.Q5, R31.Pin_0
  N46: SR_5.Q6, R32.Pin_0
  N47: SR_5.Q7, R49.Pin_0
  N48: SR_5.DS, SR_4.Q7'
  N49: SR_5.Q0, R33.Pin_0
  N50: SR_4.Q1, R39.Pin_0
  N51: SR_4.Q2, R34.Pin_0
  N52: SR_4.Q3, R40.Pin_0
  N53: SR_4.Q4, R35.Pin_0
  N54: SR_4.Q5, R36.Pin_0
  N55: SR_4.Q6, R37.Pin_0
  N56: SR_4.Q7, R38.Pin_0
  N57: SR_4.Q0, R48.Pin_0
  N58: R1.Pin_1, LED1.cathode
  N59: R2.Pin_1, LED2.cathode
  N60: LED1.anode, J8.pin1
  N61: LED2.anode, J8.pin8
  N62: IR_-_S.Vout, J8.pin7
  N63: R4.Pin_1, J2.pin3
  N64: R3.Pin_1, J2.pin9
  N65: R5.Pin_1, J2.pin4
  N66: R6.Pin_1, J2.pin5
  N67: R7.Pin_1, J2.pin6
  N68: R8.Pin_1, J2.pin7
  N69: R9.Pin_1, J2.pin8
  N70: R10.Pin_0, J7.pin2
  N71: R11.Pin_0, J7.pin8
  N72: R12.Pin_0, J7.pin5
  N73: R13.Pin_0, J7.pin4
  N74: R14.Pin_0, J7.pin3
  N75: R15.Pin_0, J7.pin7
  N76: R16.Pin_0, J7.pin6
  N77: R17.Pin_0, J6.pin8
  N78: R18.Pin_0, J6.pin7
  N79: R19.Pin_0, J6.pin6
  N80: R20.Pin_0, J6.pin5
  N81: R21.Pin_0, J6.pin4
  N82: R22.Pin_0, J9.pin2
  N83: R23.Pin_0, J9.pin7
  N84: R24.Pin_0, J9.pin6
  N85: R25.Pin_0, J9.pin5
  N86: R26.Pin_0, J9.pin4
  N87: R27.Pin_0, J9.pin1
  N88: R28.Pin_1, J3.pin8
  N89: R29.Pin_1, J3.pin6
  N90: R30.Pin_1, J3.pin5
  N91: R31.Pin_1, J3.pin4
  N92: R32.Pin_1, J3.pin3
  N93: R33.Pin_1, J3.pin9
  N94: R34.Pin_1, J4.pin7
  N95: R35.Pin_1, J4.pin5
  N96: R36.Pin_1, J4.pin4
  N97: R37.Pin_1, J4.pin3
  N98: R38.Pin_1, J4.pin2
  N99: R39.Pin_1, J4.pin8
  N100: R40.Pin_1, J4.pin6
  N101: R41.Pin_0, J9.pin3
  N102: R42.Pin_0, J6.pin2
  N103: R43.Pin_0, J6.pin3
  N104: R44.Pin_1, J3.pin7
  N105: J7.pin1, R45.Pin_0
  N106: J6.pin1, R46.Pin_0
  N107: R47.Pin_0, J9.pin8
  N108: J4.pin9, R48.Pin_1
  N109: R49.Pin_1, J3.pin2
  N110: J2.pin2, R50.Pin_1
  N111: Pad1.pad, R51.Pin_1

notes:
  Shift_out Board 2.0
  G 7 6 5 4 3 2 1 0
  0 1 2 3 4 5 6 7 G
  led1
  VCC
  GND
  DS
  ST_CP
  SH_CP
  IR DATA
  led2
  SG3
  SG4
  SG5
  SG2
  SG6
  SG1
  LED Test
