# Fritzing sketch id3734_Dado_0 (saved by Fritzing 0.9.2b)
breadboards: 1

parts:
  R1 = Resistor [tolerance=±5% resistance=220 part_number=1 package=THT]
  LED1 = Super Flux LED blue [color=Red]
  Parte1 = Arduino Uno (Rev3)
  LED2 = Super Flux LED blue [color=Red]
  R2 = Resistor [tolerance=±5% resistance=220 part_number=2 package=THT]
  LED3 = Super Flux LED blue [color=Red]
  R3 = Resistor [tolerance=±5% resistance=220 part_number=3 package=THT]
  LED4 = Super Flux LED blue [color=Red]
  R4 = Resistor [tolerance=±5% resistance=220 part_number=1 package=THT]
  LED5 = Super Flux LED blue [color=Red]
  R5 = Resistor [tolerance=±5% resistance=220 part_number=1 package=THT]
  LED6 = Super Flux LED blue [color=Red]
  R6 = Resistor [tolerance=±5% resistance=220 part_number=1 package=THT]
  S1 = Pushbutton [package=THT]
  R7 = Resistor [tolerance=±5% resistance=100k package=THT]

nets:
  N1: R1.Pin_0, Parte1.GND, R2.Pin_0, R3.Pin_0, R4.Pin_1, R5.Pin_1, R6.Pin_1, R7.Pin_1
  N2: R1.Pin_1, LED1.cathode
  N3: LED1.anode, Parte1.D2
  N4: Parte1.D8, S1.leg1, R7.Pin_0
  N5: Parte1.D3_PWM, LED2.anode
  N6: Parte1.D4, LED3.anode
  N7: Parte1.D5_PWM, LED4.anode
  N8: Parte1.D6_PWM, LED5.anode
  N9: Parte1.D7, LED6.anode
  N10: Parte1.5V, S1.leg0
  N11: LED2.cathode, R2.Pin_1
  N12: LED3.cathode, R3.Pin_1
  N13: LED4.cathode, R4.Pin_0
  N14: LED5.cathode, R5.Pin_0
  N15: LED6.cathode, R6.Pin_0
