# Fritzing sketch id3737_unplug_0 (saved by Fritzing 0.9.0b)
breadboards: 1

parts:
  Raspberry_Pi1 = Raspberry_Pi_B+
  R10 = Resistor [tolerance=±5% resistance=1k package=THT]
  S1 = Pushbutton [package="[THT]"]

nets:
  N1: Raspberry_Pi1.connector0, S1.Pin_1, S1.Pin_2
  N2: Raspberry_Pi1.connector7, R10.Pin_1
  N3: R10.Pin_0, S1.Pin_3, S1.Pin_4

notes:
  Shutdown/reboot push button for Raspberry Pi
  1x Push button 4 pins
  1x 1K Ohms resistor
  Some cables (male-female and male-male)
