# Fritzing sketch id3738_basic_electronics_2_0 (saved by Fritzing 0.9.3b)
stripboards: 1

parts:
  J2 = Basic Servo
  hc-sr1 = hc-sr04
  hc-sr2 = hc-sr04
  hc-sr3 = hc-sr04
  hc-sr4 = hc-sr04
  microSD_Transflash1 = SparkFun - microSD Transflash
  J1 = Basic Servo
  U4 = LIPO-2000mAh [package=lipo-2000]
  Part5 = adafruit [part_number="Adafruit #2542"]
  Part6 = adafruit [part_number="Adafruit #2745"]
  DJI_ESC_30A1 = DJI_30A_ESC
  DJI_ESC_30A2 = DJI_30A_ESC
  U5 = 4ChannelRelay
  R1 = Trimmer Potentiometer [maximum_resistance=10kΩ package=THT]
  Part8 = Arduino Uno (Rev3) - ICSP
  ANT1 = Antenna  # not connected
  ANT2 = Antenna  # not connected

nets:
  GND: J2.gnd, J1.gnd
  VCC: J2.vcc, hc-sr1.VCC, hc-sr2.VCC, hc-sr3.VCC, hc-sr4.VCC, microSD_Transflash1.VCC, J1.vcc, Part5.connector93, DJI_ESC_30A1.connector6, DJI_ESC_30A2.connector6, U5.connector9
  N1: hc-sr1.Trig, hc-sr1.Echo, Part8.A3
  GND_2: hc-sr1.GND, hc-sr2.GND, hc-sr3.GND, hc-sr4.GND, microSD_Transflash1.GND, Part5.connector92, Part5.connector98, DJI_ESC_30A1.connector7, DJI_ESC_30A2.connector7, U5.connector1, Part8.GND
  N2: hc-sr2.Trig, hc-sr2.Echo, Part8.A1
  N3: hc-sr3.Trig, hc-sr3.Echo, Part8.A2
  N4: hc-sr4.Trig, hc-sr4.Echo, Part8.A0
  N5: microSD_Transflash1.DO, Part8.D12/MISO
  N6: microSD_Transflash1.SCK, Part8.D13/SCK
  N7: microSD_Transflash1.DI, Part8.ICSP_MOSI, Part8.D11_PWM/MOSI
  N8: microSD_Transflash1.CS, Part8.D10_PWM/SS
  N9: U4.+, Part6.connector6, U5.connector4
  N10: U4.-, Part6.connector8
  N11: Part5.connector94, Part8.D4
  N12: Part5.connector95, Part8.D2
  N13: Part5.connector96, Part8.D3_PWM
  N14: Part6.connector7, U5.connector7, U5.connector10, Part8.VIN
  N15: DJI_ESC_30A1.connector0, DJI_ESC_30A2.connector0
  N16: DJI_ESC_30A1.connector1, DJI_ESC_30A2.connector1, U5.connector6
  N17: DJI_ESC_30A2.connector5, Part8.D5_PWM
  N18: R1.wiper, Part8.D6_PWM

notes:
  5V Always On
  5V Switched
  1kOhm
  Reverser Y Harness
