# Fritzing sketch id373_Ardufrizzing_0 (saved by Fritzing 0.7.5b)
breadboards: 1

parts:
  Arduino1 = Arduino
  LED1 = LED - 5mm [color="Red (633nm)" package="5 mm [THT]"]
  R1 = Resistor [tolerance=±5% resistance=220 package=THT]
  R2 = Resistor [tolerance=±5% resistance=220 package=THT]
  LED2 = LED - 5mm [color="Green (560nm)" package="5 mm [THT]"]
  LED3 = LED - 5mm [color="Yellow (585nm)" package="5 mm [THT]"]
  R3 = Resistor [tolerance=±5% resistance=220 package=THT]
  LED4 = LED - 5mm [color="Yellow (585nm)" package="5 mm [THT]"]
  LED5 = LED - 5mm [color="Green (560nm)" package="5 mm [THT]"]
  LED6 = LED - 5mm [color="Red (633nm)" package="5 mm [THT]"]
  R4 = Resistor [tolerance=±5% resistance=220 package=THT]
  R5 = Resistor [tolerance=±5% resistance=220 package=THT]
  R6 = Resistor [tolerance=±5% resistance=220 package=THT]

nets:
  N1: Arduino1.D13, LED3.anode
  N2: Arduino1.D12, LED2.anode
  N3: Arduino1.D11, LED1.anode
  N4: Arduino1.D10, LED4.anode
  N5: Arduino1.D9, LED5.anode
  N6: Arduino1.D8, LED6.anode
  N7: LED1.cathode, R3.Pin_1
  N8: R1.Pin_0, R2.Pin_0, R3.Pin_0
  N9: R1.Pin_1, LED3.cathode
  N10: R2.Pin_1, LED2.cathode
  N11: LED4.cathode, R4.Pin_1
  N12: LED5.cathode, R5.Pin_1
  N13: LED6.cathode, R6.Pin_1
  N14: R4.Pin_0, R5.Pin_0, R6.Pin_0
