# Fritzing sketch id3740_[SIA_201701]_DAMP_3rd_week_02_0 (saved by Fritzing 0.9.3b)
breadboards: 1

parts:
  부품1 = Arduino Uno (Rev3)
  LED1 = RGB LED (com. cathode, rgb) [package="5 mm [THT]"]

nets:
  N1: 부품1.GND, LED1.red_anode
  N2: 부품1.D3_PWM, LED1.blue_anode
  N3: 부품1.D5_PWM, LED1.green_anode
  N4: 부품1.D6_PWM, LED1.common_cathode
