# Fritzing sketch id3742_[SIA_201701]_DAMP_4th_week_02_0 (saved by Fritzing 0.9.3b)
breadboards: 1

parts:
  부품1 = Arduino Uno (Rev3)
  U1 = POT [package=pot_mammoth]

nets:
  N1: 부품1.A0, U1.A
  N2: 부품1.5V, U1.E
  N3: 부품1.GND, U1.S
