# Fritzing sketch id3743_[SIA_201701]_DAMP_5th_week_01_0 (saved by Fritzing 0.9.3b)
breadboards: 1

parts:
  부품1 = Arduino Uno (Rev3)
  J1 = Basic Servo
  LED1 = LED - 5mm [color="Red (633nm)" package="5 mm [THT]"]

nets:
  N1: 부품1.D13/SCK, LED1.anode
  N2: 부품1.D6_PWM, J1.pulse
  5V: 부품1.5V, J1.vcc
  GND: 부품1.GND, J1.gnd, LED1.cathode
