# Fritzing sketch id3744_[SIA_201701]_DAMP_6th_week_01_0 (saved by Fritzing 0.9.3b)

parts:
  부품1 = Arduino Uno (Rev3)
  부품2 = Soil Moisture Sensor

nets:
  N1: 부품1.A0, 부품2.SIG
  5V: 부품1.5V, 부품2.VCC
  GND: 부품1.GND, 부품2.GND
