# Fritzing sketch id3745_fritzing (saved by Fritzing 0.9.3b)
breadboards: 1

parts:
  Part2 = RFID-RC522
  Part1 = Arduino Uno (Rev3) - ICSP
  LED1 = LED - 3mm [color="Red (633nm)" package="3 mm [THT]"]
  LED2 = LED - 3mm [color="Green (555nm)" package="3 mm [THT]"]
  LED3 = LED - 3mm [color="Blue (430nm)" package="3 mm [THT]"]
  R1 = Resistor [tolerance=±5% resistance=220 package="0402 [SMD]"]
  R2 = Resistor [tolerance=±5% resistance=220 package="0402 [SMD]"]
  R3 = Resistor [tolerance=±5% resistance=220 package="0402 [SMD]"]
  S1 = Pushbutton [package="[THT]"]
  R4 = Resistor [tolerance=±5% resistance=10k package="0402 [SMD]"]
  KY-1 = keyes
  LCM1602_IIC1 = generic_ic_dip_22_300mil.fzp [part_number="LCM1602 IIC" chip_label="LCM1602 IIC"]
  LCD1 = LCD screen

nets:
  N1: Part2.connector8, Part1.D10_PWM/SS
  N2: Part2.connector9, Part1.D13/SCK
  N3: Part2.connector10, Part1.D11_PWM/MOSI
  N4: Part2.connector11, Part1.D12/MISO
  N5: Part2.connector13, Part1.GND, LED1.cathode, LED2.cathode, LED3.cathode, R4.Pin_1, KY-1.connector2, LCM1602_IIC1.connector16
  N6: Part2.connector14, Part1.D9_PWM
  N7: Part2.connector15, Part1.3V3
  N8: Part1.A4/SDA, LCM1602_IIC1.connector18
  N9: Part1.A5/SCL, LCM1602_IIC1.connector19
  N10: Part1.5V, S1.Pin_3, S1.Pin_4, KY-1.connector1, LCM1602_IIC1.connector17
  N11: Part1.D3_PWM, S1.Pin_1, S1.Pin_2, R4.Pin_0
  N12: Part1.D4, KY-1.connector0
  N13: Part1.D5_PWM, LED3.anode, R3.Pin_0, R3.Pin_1
  N14: Part1.D6_PWM, LED2.anode, R2.Pin_0, R2.Pin_1
  N15: Part1.D7, LED1.anode, R1.Pin_0, R1.Pin_1
  N16: LCM1602_IIC1.connector0, LCD1.VSS
  N17: LCM1602_IIC1.connector1, LCD1.VDD
  N18: LCM1602_IIC1.connector2, LCD1.V0
  N19: LCM1602_IIC1.connector3, LCD1.RS
  N20: LCM1602_IIC1.connector4, LCD1.R/W
  N21: LCM1602_IIC1.connector5, LCD1.E
  N22: LCM1602_IIC1.connector6, LCD1.DB0
  N23: LCM1602_IIC1.connector7, LCD1.DB1
  N24: LCM1602_IIC1.connector8, LCD1.DB2
  N25: LCM1602_IIC1.connector9, LCD1.DB3
  N26: LCM1602_IIC1.connector10, LCD1.DB4
  N27: LCM1602_IIC1.connector11, LCD1.DB5
  N28: LCM1602_IIC1.connector12, LCD1.DB6
  N29: LCM1602_IIC1.connector13, LCD1.DB7
  N30: LCM1602_IIC1.connector14, LCD1.LED+
  N31: LCM1602_IIC1.connector15, LCD1.LED-
  N32: LCM1602_IIC1.connector20, LCM1602_IIC1.connector21
