# Fritzing sketch id3746_SignalR_on_RaspPi_0 (saved by Fritzing 0.9.1b)
breadboards: 1

parts:
  Raspberry_Pi1 = Raspberry Pi B+
  R1 = Resistor [tolerance=±5% resistance=270 package=THT]
  S1 = Pushbutton [package="[THT]"]
  R2 = Resistor [tolerance=±5% resistance=10k package=THT]
  LED1 = LED - 5mm [color="Yellow (595nm)" part_number=a package="5 mm [THT]"]

nets:
  N1: Raspberry_Pi1.3v3, S1.Pin_3, S1.Pin_4
  N2: Raspberry_Pi1.GND, R1.Pin_1, R2.Pin_1
  N3: Raspberry_Pi1.GPIO25, LED1.anode
  N4: Raspberry_Pi1.GPIO24, S1.Pin_1, S1.Pin_2, R2.Pin_0
  N5: R1.Pin_0, LED1.cathode
