# Fritzing sketch id3747_SigZBDec_V1_0_0 (saved by Fritzing 0.9.2b)
circuit board: 3.6cm x 3.2cm
breadboards: 1

parts:
  R1 = Resistor [tolerance=±1% resistance=10k package="0805 [SMD]"]
  R2 = Resistor [tolerance=±1% resistance=10k package="0805 [SMD]"]
  D2 = 1N4007
  IC1 = ATtiny24-44-84
  IC2 = 78L05
  C1 = Ceramic Capacitor [capacitance=100nF package="0805 [SMD, multilayer]"]
  C2 = Tantalum Capacitor [capacitance=10µF voltage=35V package="D 7343 [SMD, tantalum]"]
  R3 = Resistor [tolerance=±1% resistance=10k package="0805 [SMD]"]
  R4 = Resistor [tolerance=±1% resistance=47 package="0805 [SMD]"]
  D3 = 1N4007
  D4 = 1N4007
  D5 = 1N4007
  D6 = 1N4007
  C3 = Ceramic Capacitor [capacitance=100nF package="0805 [SMD, multilayer]"]
  R5 = Resistor [tolerance=±1% resistance=680 package="0805 [SMD]"]
  R6 = Resistor [tolerance=±1% resistance=47 package="0805 [SMD]"]
  U1 = TRIAC [package=sot223]
  X1 = smd_Stiftleiste_8
  IC3 = LTV814S
  D1 = Rectifier Diode [breakdown_voltage=4.7V part_number=4,7V package="Melf DO-213 AA [SMD]"]
  IC4 = MOC3021
  X2 = smd_Stiftleiste_2
  X3 = smd_Stiftleiste_3

nets (from the pcb view):
  N1: R1.Pin_0, IC1.connector3, X1.connector0
  N2: R1.Pin_1, IC1.connector0, IC2.connector0, C1.1, R3.Pin_1, X1.connector1
  N3: R2.Pin_0, IC1.connector5, D1.cathode
  N4: R2.Pin_1, D2.connector0, X2.connector0, X3.connector3
  N5: D2.connector1, IC2.connector2, C2.+
  N6: IC1.connector4, R5.Pin_1
  N7: IC1.connector6, X1.connector6
  N8: IC1.connector7, X1.connector5
  N9: IC1.connector8, X1.connector4
  N10: IC1.connector9, R3.Pin_0, C3.1, IC3.connector3
  N11: IC1.connector10, X1.connector3
  N12: IC1.connector11, X1.connector2
  N13: IC1.connector13, IC2.connector1, C1.0, C2.-, C3.0, IC4.connector1
  N14: IC2.connector3, U1.M1, X1.connector7, IC3.connector2, D1.anode, X2.connector1, X3.connector1
  N15: R4.Pin_0, IC3.connector0
  N16: R4.Pin_1, D4.connector1, D6.connector0, X3.connector0
  N17: D3.connector0, D5.connector1, R6.Pin_1, U1.M2, IC3.connector1
  N18: D3.connector1, D4.connector0
  N19: D5.connector0, D6.connector1
  N20: R5.Pin_0, IC4.connector0
  N21: R6.Pin_0, IC4.connector5
  N22: U1.G, IC4.connector3

notes:
  Spannungsversorgung
  Zugbeeinflußung
  Gleisbesetztmelder
  DCC
  Signal
  ©Robert Schmitt
  V1.0
