# Fritzing sketch id3748_ESPUSB_C0_0 (saved by Fritzing 0.9.3b)
circuit board: 4.59849cm x 2.49cm
breadboards: 1

parts:
  U1 = ESP8266 WiFi Module [part_number=ESP8266]
  Pad9 = Pad [width=1.1899999999999999 height=2.2138150591353654 connect=center]  # not connected
  Pad11 = Pad [width=1.1899999999999999 height=2.2138150591353654 connect=center]  # not connected
  Pad12 = Pad [width=1.1899999999999999 height=2.2138150591353654 connect=center]  # not connected
  Pad13 = Pad [width=1.1899999999999999 height=2.2138150591353654 connect=center]  # not connected
  Pad14 = Pad [width=1.1899999999999999 height=2.2138150591353654 connect=center]  # not connected
  Pad15 = Pad [width=1.1899999999999999 height=2.2138150591353654 connect=center]  # not connected
  X1 = USB Connectors [package=usb-a-h]
  R2 = Resistor [tolerance=±5% resistance=1k package="0805 [SMD]"]
  R1 = Resistor [tolerance=±5% resistance=1k package="0805 [SMD]"]
  IC1 = CH340-SO16 [chip_label=CH340]
  C1 = Ceramic Capacitor [capacitance=22pF package="0603 [SMD, multilayer]"]
  C2 = Ceramic Capacitor [capacitance=22pF package="0603 [SMD, multilayer]"]
  Y1 = Resonator [package=resonator-smd]
  IC2 = AMS1117

nets (from the pcb view):
  N1: U1.RXD, IC1.connector1
  N2: U1.VCC, R1.Pin_1, IC1.connector15, IC2.connector1
  N3: U1.GPIO_0, IC1.connector12
  N4: U1.CH_PD, R1.Pin_0
  N5: U1.GND, R2.Pin_1
  N6: U1.TXD, IC1.connector2
  N7: U1.GPIO_15, R2.Pin_0
  N8: U1.REST, IC1.connector13
  N9: X1.D-, IC1.connector5
  N10: X1.D+, IC1.connector4
  N11: X1.VBUS, IC2.connector2
  N12: X1.GND, IC1.connector0, C1.0, C2.0, Y1.2, IC2.connector0
  N13: IC1.connector6, C1.1, Y1.3
  N14: IC1.connector7, C2.1, Y1.1

notes:
  Reset
  ADC
  CH_PD
  GPIO16
  GPIO14
  GPIO12
  GPIO13
  VCC
  GND
  GPIO15
  GPIO0
  GPIO5
  GPIO4
  RX
  TX
  GPIO11
  GPIO6
  GPIO8
  GPIO10
  GPIO7
  GPIO9
  GPIO2
  3v3
