# Fritzing sketch id3749_SIM3U166_B_GQ_0 (saved by Fritzing 0.9.1b)
circuit board: 8.4cm x 2.8cm
breadboards: 1

parts:
  J2 = rounded female pin header, 32 pins [form="♀ (female rounded)"]
  J1 = rounded female pin header, 32 pins [form="♀ (female rounded)"]
  U1 = SIM3U166-B-GQ

nets:
  N1: J2.pin1, U1.connector63
  N2: J2.pin2, U1.connector62
  N3: J2.pin3, U1.connector61
  N4: J2.pin4, U1.connector60
  N5: J2.pin5, U1.connector59
  N6: J2.pin6, U1.connector58
  N7: J2.pin7, U1.connector57
  N8: J2.pin8, U1.connector56
  N9: J2.pin9, U1.connector55
  N10: J2.pin10, U1.connector54
  N11: J2.pin11, U1.connector53
  N12: J2.pin12, U1.connector52
  N13: J2.pin13, U1.connector51
  N14: J2.pin14, U1.connector50
  N15: J2.pin15, U1.connector49
  N16: J2.pin16, U1.connector48
  N17: J2.pin17, U1.connector47
  N18: J2.pin18, U1.connector46
  N19: J2.pin19, U1.connector45
  N20: J2.pin20, U1.connector44
  N21: J2.pin21, U1.connector43
  N22: J2.pin22, U1.connector42
  N23: J2.pin23, U1.connector41
  N24: J2.pin24, U1.connector40
  N25: J2.pin25, U1.connector39
  N26: J2.pin26, U1.connector38
  N27: J2.pin27, U1.connector37
  N28: J2.pin28, U1.connector36
  N29: J2.pin29, U1.connector35
  N30: J2.pin30, U1.connector34
  N31: J2.pin31, U1.connector33
  N32: J2.pin32, U1.connector32
  N33: J1.pin1, U1.connector0
  N34: J1.pin2, U1.connector1
  N35: J1.pin3, U1.connector2
  N36: J1.pin4, U1.connector3
  N37: J1.pin5, U1.connector4
  N38: J1.pin6, U1.connector5
  N39: J1.pin7, U1.connector6
  N40: J1.pin8, U1.connector7
  N41: J1.pin9, U1.connector8
  N42: J1.pin10, U1.connector9
  N43: J1.pin11, U1.connector10
  N44: J1.pin12, U1.connector11
  N45: J1.pin13, U1.connector12
  N46: J1.pin14, U1.connector13
  N47: J1.pin15, U1.connector14
  N48: J1.pin16, U1.connector15
  N49: J1.pin17, U1.connector16
  N50: J1.pin18, U1.connector17
  N51: J1.pin19, U1.connector18
  N52: J1.pin20, U1.connector19
  N53: J1.pin21, U1.connector20
  N54: J1.pin22, U1.connector21
  N55: J1.pin23, U1.connector22
  N56: J1.pin24, U1.connector23
  N57: J1.pin25, U1.connector24
  N58: J1.pin26, U1.connector25
  N59: J1.pin27, U1.connector26
  N60: J1.pin28, U1.connector27
  N61: J1.pin29, U1.connector28
  N62: J1.pin30, U1.connector29
  N63: J1.pin31, U1.connector30
  N64: J1.pin32, U1.connector31

notes:
  PB4.3
  VSSHD
  PB4.2
  PB4.1
  PB4.0
  PB3.9
  PB3.7
  PB3.6
  PB4.
  PB3.5
  PB3.4
  PB3.3
  PB3.2
  VIOHD
  PB3.1
  PB3.0
  PB2.3
  PB2.2
  PB2.0
  PB1.15
  PB2.1
  PB2.
  VIO
  PB1.13
  PB1.7
  PB1.14
  VSS
  PB1.12
  PB1.10
  PB1.11
  PB1.9
  PB1.6
  PB1.8
  PB1.5
  PB1.4
  SWCLK
  PB1.0
  SWDIO
  PB1.3
  PB1.2
  PB1.1
  PB0.15
  PB0.14
  PB0.13
  PB0.12
  PB0.11
  PB0.10
  PB0.8
  PB0.7
  PB0.9
  PB0.6
  PB0.5
  PB0.4
  PB0.3
  PB0.2
  PB0.1
  PB0.0
  VDD
  D+
  VVREGN
  VBUS
  D-
  _RESET_
  Created by Scott Marchant  - 2015
  In honor of Professor Don Cripps
  Utah State University - ECE
  SIM3U166-B-GQ
  http://fritzing.org/projects/sim3u166-b-gq-breadboard-adapter
  PB3.8
  Scott Marchant - 2015
  SIM3U166-B-GQ Breadboard Adapter
  License: CC BY-SA 3.0
