# Fritzing sketch id374_Semaforo_Fritzing_0 (saved by Fritzing 0.9.1b)
breadboards: 1

parts:
  Parte1 = Arduino BT
  R1 = Resistor [tolerance=±5% resistance=220 package=THT]
  LED1 = LED - 5mm [color="Red (633nm)" package="5 mm [THT]"]
  R2 = Resistor [tolerance=±5% resistance=220 package=THT]
  R3 = Resistor [tolerance=±5% resistance=220 package=THT]
  LED2 = LED - 5mm [color="Orange (620nm)" package="5 mm [THT]"]
  LED3 = LED - 5mm [color="Green (555nm)" package="5 mm [THT]"]

nets:
  N1: Parte1.MOSI/PWM_D11, LED3.anode
  N2: Parte1.MISO/D12, LED2.anode
  N3: Parte1.SCK/D13, LED1.anode
  N4: Parte1.GND, R1.Pin_0, R2.Pin_0, R3.Pin_0
  N5: R1.Pin_1, LED1.cathode
  N6: R2.Pin_1, LED2.cathode
  N7: R3.Pin_1, LED3.cathode
