# Fritzing sketch id3750_SimonLed_0 (saved by Fritzing 0.8.3b)
breadboards: 1

parts:
  Arduino1 = Arduino
  R1 = Resistor [tolerance=±5% resistance=220 package=THT]
  R2 = Resistor [tolerance=±5% resistance=220 package=THT]
  R3 = Resistor [tolerance=±5% resistance=220 package=THT]
  LED1 = LED - 5mm [color="Red (633nm)" package="5 mm [THT]"]
  LED2 = LED - 5mm [color="Yellow (592nm)" package="5 mm [THT]"]
  LED3 = LED - 5mm [color="Green (570nm)" package="5 mm [THT]"]
  J1 = Piezo Speaker
  S1 = Pushbutton [package="[THT]"]
  S2 = Pushbutton [package="[THT]"]
  S3 = Pushbutton [package="[THT]"]

nets:
  N1: Arduino1.GND, R1.Pin_1, R2.Pin_1, R3.Pin_1, LED1.cathode, LED1.anode, LED2.cathode, LED2.anode, LED3.cathode, LED3.anode, J1.pin1, S1.Pin_3, S1.Pin_4, S2.Pin_3, S2.Pin_4, S3.Pin_3, S3.Pin_4
  N2: Arduino1.D12, R2.Pin_0
  N3: Arduino1.D11, R3.Pin_0
  N4: Arduino1.D10, R1.Pin_0
  N5: Arduino1.D7, S3.Pin_1, S3.Pin_2
  N6: Arduino1.D6, S2.Pin_1, S2.Pin_2
  N7: Arduino1.D5, S1.Pin_1, S1.Pin_2
  N8: Arduino1.D2, J1.pin2
