# Fritzing sketch id3751_simon_0 (saved by Fritzing 0.9.3b)
breadboards: 1

parts:
  LED1 = LED - 3mm [color="Red (633nm)" package="3 mm [THT]"]
  LED2 = LED - 3mm [color="Green (555nm)" package="3 mm [THT]"]
  LED3 = LED - 3mm [color="Blue (430nm)" package="3 mm [THT]"]
  LED4 = LED - 3mm [color="Yellow (595nm)" package="3 mm [THT]"]
  R2 = Resistor [tolerance=±5% resistance=220 package=THT]
  R3 = Resistor [tolerance=±5% resistance=220 package=THT]
  R1 = Resistor [tolerance=±5% resistance=100 package=THT]
  R4 = Resistor [tolerance=±5% resistance=220 package=THT]
  S1 = Pushbutton [package="[THT]"]
  S2 = Pushbutton [package="[THT]"]
  S3 = Pushbutton [package="[THT]"]
  S4 = Pushbutton [package="[THT]"]
  J1 = Piezo Speaker
  Bauteil1 = Arduino Mega 2560 (Rev3)

nets:
  N1: LED1.cathode, Bauteil1.D13_PWM
  N2: LED1.anode, R3.Pin_0
  N3: LED2.cathode, Bauteil1.D12_PWM
  N4: LED2.anode, R2.Pin_0
  N5: LED3.cathode, Bauteil1.D11_PWM
  N6: LED3.anode, R1.Pin_0
  N7: LED4.cathode, Bauteil1.D10_PWM
  N8: LED4.anode, R4.Pin_0
  N9: R2.Pin_1, R3.Pin_1, R1.Pin_1, R4.Pin_1, S1.Pin_1, S1.Pin_2, S2.Pin_1, S2.Pin_2, S3.Pin_1, S3.Pin_2, S4.Pin_1, S4.Pin_2, Bauteil1.GND
  N10: S1.Pin_3, S1.Pin_4, Bauteil1.D7_PWM
  N11: S2.Pin_3, S2.Pin_4, Bauteil1.D6_PWM
  N12: S3.Pin_3, S3.Pin_4, Bauteil1.D5_PWM
  N13: S4.Pin_3, S4.Pin_4, Bauteil1.D4_PWM
  N14: J1.pin1, Bauteil1.D3_PWM
  N15: J1.pin2, Bauteil1.D8_PWM
