# Fritzing sketch id3754_SimpeACCUlKeyer_0 (saved by Fritzing 0.9.1b)
circuit board: 8.46667cm x 5.64444cm
breadboards: 1

parts:
  Part1 = Arduino Uno (Rev3)
  LED1 = LED - 5mm [color="Red (633nm)" package="5 mm [THT]"]
  R2 = Resistor [tolerance=±5% resistance=10k package=THT]
  R3 = Resistor [tolerance=±5% resistance=10k package=THT]
  SPEAKER = Piezo Speaker
  DIN_Connector = XLR3_NCFAH2 [package=xlr3_nc3fah2]
  R6 = Resistor [tolerance=±5% resistance=390 package=THT]
  R7 = Rotary Potentiometer (Small) [maximum_resistance=100kΩ package=THT]
  R8 = Resistor [tolerance=±5% resistance=100 package=THT]

nets:
  N1: Part1.A3, R7.wiper
  N2: Part1.D9_PWM, R2.Pin_1, DIN_Connector.2
  N3: Part1.D10_PWM/SS, R3.Pin_1, DIN_Connector.1
  N4: Part1.D13/SCK, R6.Pin_1
  N5: Part1.GND, LED1.cathode, SPEAKER.pin1, R7.leg2
  N6: Part1.D3_PWM, R8.Pin_1
  N7: Part1.5V, R2.Pin_0, R3.Pin_0, R7.leg1
  N8: LED1.anode, R6.Pin_0
  N9: SPEAKER.pin2, R8.Pin_0
