# Fritzing sketch id3755_one_led_+_RBPI3_0 (saved by Fritzing 0.9.3b)
breadboards: 1

parts:
  LED1 = LED - 5mm [color="Red (633nm)" package="5 mm [THT]"]
  R1 = Resistor [tolerance=±5% resistance=220 package=THT]
  Raspberry_Pi_1 = Raspberry Pi 3 [part_number=RPI-3-V1.2]

nets:
  N1: LED1.cathode, Raspberry_Pi_1.GND
  N2: LED1.anode, R1.Pin_1
  N3: R1.Pin_0, Raspberry_Pi_1.GIPO17
