# Fritzing sketch id3756_MyThing_0 (saved by Fritzing 0.9.0b)
breadboards: 1

parts:
  U1 = 74HC595 [package="DIP16 [THT]"]
  R1 = Resistor [tolerance=±5% resistance=220 package=THT]
  R2 = Resistor [tolerance=±5% resistance=220 package=THT]
  R3 = Resistor [tolerance=±5% resistance=220 package=THT]
  R4 = Resistor [tolerance=±5% resistance=220 package=THT]
  7_Segment_4_Digit_Display1 = MyPart1 [part_number=HS420561K-32]
  Part1 = Arduino Uno (Rev3)
  T1 = TMP36 Temperature Sensor [package="TO92 [THT]"]

nets:
  N1: U1.Q1, 7_Segment_4_Digit_Display1.connector7
  N2: U1.Q2, 7_Segment_4_Digit_Display1.connector4
  N3: U1.Q3, 7_Segment_4_Digit_Display1.connector2
  N4: U1.Q4, 7_Segment_4_Digit_Display1.connector1
  N5: U1.Q5, 7_Segment_4_Digit_Display1.connector10
  N6: U1.Q6, 7_Segment_4_Digit_Display1.connector5
  N7: U1.Q7, 7_Segment_4_Digit_Display1.connector3
  GND: U1.GND, U1.OE, Part1.GND, T1.GND
  N8: U1.SH_CP, Part1.D10_PWM/SS
  N9: U1.ST_CP, Part1.D9_PWM
  N10: U1.DS, Part1.D8
  N11: U1.Q0, 7_Segment_4_Digit_Display1.connector11
  VCC: U1.VCC, Part1.5V, T1.+Vs
  N12: R1.Pin_0, Part1.D5_PWM
  N13: R1.Pin_1, 7_Segment_4_Digit_Display1.connector12
  N14: R2.Pin_0, Part1.D4
  N15: R2.Pin_1, 7_Segment_4_Digit_Display1.connector9
  N16: R3.Pin_0, Part1.D3_PWM
  N17: R3.Pin_1, 7_Segment_4_Digit_Display1.connector8
  N18: R4.Pin_0, Part1.D2
  N19: R4.Pin_1, 7_Segment_4_Digit_Display1.connector6
  N20: Part1.A0, T1.Vout
