# Fritzing sketch id3757_relay_0 (saved by Fritzing 0.9.0b)
circuit board: 7.57858cm x 7.81242cm

parts:
  LED1 = LED - 5mm [color="Green (570nm)" package="5 mm [THT]"]
  LED2 = LED - 5mm [color="Green (570nm)" package="5 mm [THT]"]
  LED3 = LED - 5mm [color="Green (570nm)" package="5 mm [THT]"]
  LED4 = LED - 5mm [color="Green (570nm)" package="5 mm [THT]"]
  R1 = Resistor [tolerance=±5% resistance=220 package=THT]
  R2 = Resistor [tolerance=±5% resistance=220 package=THT]
  R3 = Resistor [tolerance=±5% resistance=220 package=THT]
  R4 = Resistor [tolerance=±5% resistance=220 package=THT]
  Relay2 = Relay_T73
  Relay3 = Relay_T73
  Relay1 = Relay_T73
  Relay4 = Relay_T73
  Q1 = PNP-Transistor [package="TO92 [THT]"]
  Q2 = PNP-Transistor [package="TO92 [THT]"]
  Q3 = PNP-Transistor [package="TO92 [THT]"]
  Q4 = PNP-Transistor [package="TO92 [THT]"]
  LED5 = LED - 5mm [color="Red (633nm)" package="5 mm [THT]"]
  R5 = Resistor [tolerance=±5% resistance=220 package=THT]
  D1 = Rectifier Diode [part_number=1N4001 package="300 mil [THT]"]
  D2 = Rectifier Diode [part_number=1N4001 package="300 mil [THT]"]
  D3 = Rectifier Diode [part_number=1N4001 package="300 mil [THT]"]
  D4 = Rectifier Diode [part_number=1N4001 package="300 mil [THT]"]
  J5 = screw terminal, 4 pins
  J6 = Screw terminal - 2 pins [package=THT]
  J1 = screw terminal, 3 pins
  J2 = screw terminal, 3 pins
  J3 = screw terminal, 3 pins
  J4 = screw terminal, 3 pins

nets:
  N1: LED1.cathode, R1.Pin_1
  N2: LED1.anode, Relay1.connector0, Q1.E, D1.cathode
  N3: LED2.cathode, R2.Pin_1
  N4: LED2.anode, Relay2.connector0, Q2.E, D2.cathode
  N5: LED3.cathode, R3.Pin_1
  N6: LED3.anode, Relay3.connector0, Q3.E, D3.cathode
  N7: LED4.cathode, R4.Pin_0
  N8: LED4.anode, Relay4.connector0, Q4.E, D4.cathode
  N9: R1.Pin_0, R2.Pin_0, R3.Pin_0, R4.Pin_1, Relay2.connector1, Relay3.connector1, Relay1.connector1, Relay4.connector1, R5.Pin_1, D1.anode, D2.anode, D3.anode, D4.anode, J6.pin1
  N10: Relay2.connector2, J2.pin2
  N11: Relay2.connector3, J2.pin3
  N12: Relay2.connector4, J2.pin1
  N13: Relay3.connector2, J3.pin2
  N14: Relay3.connector3, J3.pin3
  N15: Relay3.connector4, J3.pin1
  N16: Relay1.connector2, J1.pin2
  N17: Relay1.connector3, J1.pin3
  N18: Relay1.connector4, J1.pin1
  N19: Relay4.connector2, J4.pin2
  N20: Relay4.connector3, J4.pin3
  N21: Relay4.connector4, J4.pin1
  N22: Q1.B, J5.pin4
  N23: Q1.C, Q2.C, Q3.C, Q4.C, LED5.anode, J6.pin2
  N24: Q2.B, J5.pin3
  N25: Q3.B, J5.pin2
  N26: Q4.B, J5.pin1
  N27: LED5.cathode, R5.Pin_0

notes:
  www.enCypher.in
