# Fritzing sketch id3758_74HC165_diagram_0 (saved by Fritzing 0.9.3b)
breadboards: 1

parts:
  U2 = 74HC595 [part_number=SN74LS165]
  Part3 = Arduino Uno (Rev3)
  S1 = Pushbutton [package="[THT]"]
  S2 = Pushbutton [package="[THT]"]
  S3 = Pushbutton [package="[THT]"]
  S4 = Pushbutton [package="[THT]"]
  S5 = Pushbutton [package="[THT]"]
  S6 = Pushbutton [package="[THT]"]
  S7 = Pushbutton [package="[THT]"]
  S8 = Pushbutton [package="[THT]"]
  R1 = Resistor [tolerance=±5% resistance=10k package=THT]
  R2 = Resistor [tolerance=±5% resistance=10k package=THT]
  R3 = Resistor [tolerance=±5% resistance=10k package=THT]
  R4 = Resistor [tolerance=±5% resistance=10k package=THT]
  R5 = Resistor [tolerance=±5% resistance=10k package=THT]
  R7 = Resistor [tolerance=±5% resistance=10k package=THT]
  R8 = Resistor [tolerance=±5% resistance=10k package=THT]
  R9 = Resistor [tolerance=±5% resistance=10k package=THT]

nets:
  N1: U2.connector0, Part3.D8
  N2: U2.connector1, Part3.D12/MISO
  N3: U2.connector2, S5.Pin_3, S5.Pin_4, R5.Pin_0
  N4: U2.connector3, S6.Pin_3, S6.Pin_4, R9.Pin_0
  N5: U2.connector4, S7.Pin_3, S7.Pin_4, R7.Pin_0
  N6: U2.connector5, S8.Pin_3, S8.Pin_4, R8.Pin_0
  N7: U2.connector7, Part3.GND, R1.Pin_1, R2.Pin_1, R3.Pin_1, R4.Pin_1, R5.Pin_1, R7.Pin_1, R8.Pin_1, R9.Pin_1
  N8: U2.connector8, Part3.D11_PWM/MOSI
  N9: U2.connector10, S1.Pin_3, S1.Pin_4, R1.Pin_0
  N10: U2.connector11, S2.Pin_3, S2.Pin_4, R2.Pin_0
  N11: U2.connector12, S3.Pin_3, S3.Pin_4, R3.Pin_0
  N12: U2.connector13, S4.Pin_3, S4.Pin_4, R4.Pin_0
  N13: U2.connector14, Part3.D9_PWM
  N14: U2.connector15, Part3.5V, S1.Pin_1, S1.Pin_2, S2.Pin_1, S2.Pin_2, S3.Pin_1, S3.Pin_2, S4.Pin_1, S4.Pin_2, S5.Pin_1, S5.Pin_2, S6.Pin_1, S6.Pin_2, S7.Pin_1, S7.Pin_2, S8.Pin_1, S8.Pin_2
