# Fritzing sketch id3759_MIDI_Out_0 (saved by Fritzing 0.7.10b)
breadboards: 1

parts:
  Arduino1 = Arduino
  DIN1 = DIN-5 jack (MIDI) [package=THT]
  R1 = Resistor [tolerance=±5% resistance=220 package="0805 [SMD]"]

nets:
  N1: Arduino1.D1TX, DIN1.5
  N2: Arduino1.+5V, R1.Pin_0
  N3: Arduino1.GND, DIN1.2
  N4: DIN1.4, R1.Pin_1
