# Fritzing sketch id375_Arduino_1_0 (saved by Fritzing 0.9.2b)
breadboards: 1

parts:
  LED1 = LED - 5mm [color="Red (633nm)" package="5 mm [THT]"]
  R1 = Resistor [tolerance=±5% resistance=220 package=THT]
  R2 = Rotary Potentiometer (Small) [maximum_resistance=100kΩ package=THT]
  Parte1 = Arduino Uno (Rev3)

nets:
  N1: LED1.cathode, R2.leg1, R2.leg2, Parte1.GND
  N2: LED1.anode, R1.Pin_0
  N3: R1.Pin_1, Parte1.D7
  N4: R2.wiper, Parte1.A0
