# Fritzing sketch id3760_Battery_Charge_Monitor_0 (saved by Fritzing 0.9.2b)
breadboards: 1

parts:
  Componente1 = Intel Galileo Gen2
  D1 = SOLAR-IXYS [package=solarbit-12x1]
  R1 = Resistor [tolerance=±5% resistance=10k package="0402 [SMD]"]
  R2 = Resistor [tolerance=±5% resistance=10k package="0402 [SMD]"]
  VCC1 = Battery
  D3 = Rectifier Diode [part_number=1N4001 package="300 mil [THT]"]
  U1 = RELAY [package=relay-g5q]

nets:
  N1: Componente1.A0, R1.Pin_1, R2.Pin_0
  N2: Componente1.D8, U1.COIL1
  N3: Componente1.GND, D1.A, R2.Pin_1, VCC1.-, U1.NC
  N4: D1.C, U1.MAIN
  N5: R1.Pin_0, VCC1.+, D3.anode
  N6: D3.cathode, U1.COIL2
