# Fritzing sketch id3761_binary_clock_0 (saved by Fritzing 0.9.1b)
breadboards: 2

parts:
  Part1 = Arduino Uno (Rev3)
  LED6 = LED - 5mm [color="Red (633nm)" package="5 mm [THT]"]
  LED8 = LED - 5mm [color="Blue (430nm)" package="5 mm [THT]"]
  LED10 = LED - 5mm [color="Blue (430nm)" package="5 mm [THT]"]
  LED18 = LED - 5mm [color="Green (555nm)" package="5 mm [THT]"]
  LED19 = LED - 5mm [color="Red (633nm)" package="5 mm [THT]"]
  LED20 = LED - 5mm [color="Red (633nm)" package="5 mm [THT]"]
  LED21 = LED - 5mm [color="Red (633nm)" package="5 mm [THT]"]
  LED22 = LED - 5mm [color="Red (633nm)" package="5 mm [THT]"]
  LED23 = LED - 5mm [color="Red (633nm)" package="5 mm [THT]"]
  R1 = Resistor [tolerance=±5% resistance=220 package=THT]
  R2 = Resistor [tolerance=±5% resistance=220 package=THT]
  R3 = Resistor [tolerance=±5% resistance=220 package=THT]
  R4 = Resistor [tolerance=±5% resistance=220 package=THT]
  R5 = Resistor [tolerance=±5% resistance=220 package=THT]
  R6 = Resistor [tolerance=±5% resistance=220 package=THT]
  LED24 = LED - 5mm [color="Blue (430nm)" package="5 mm [THT]"]
  LED25 = LED - 5mm [color="Blue (430nm)" package="5 mm [THT]"]
  LED26 = LED - 5mm [color="Blue (430nm)" package="5 mm [THT]"]
  LED27 = LED - 5mm [color="Blue (430nm)" package="5 mm [THT]"]
  LED28 = LED - 5mm [color="Green (555nm)" package="5 mm [THT]"]
  LED29 = LED - 5mm [color="Green (555nm)" package="5 mm [THT]"]
  LED30 = LED - 5mm [color="Green (555nm)" package="5 mm [THT]"]
  LED31 = LED - 5mm [color="Green (555nm)" package="5 mm [THT]"]
  R7 = Resistor [tolerance=±5% resistance=220 package=THT]
  R8 = Resistor [tolerance=±5% resistance=220 package=THT]
  R9 = Resistor [tolerance=±5% resistance=220 package=THT]
  R10 = Resistor [tolerance=±5% resistance=220 package=THT]
  R11 = Resistor [tolerance=±5% resistance=220 package=THT]
  R12 = Resistor [tolerance=±5% resistance=220 package=THT]
  R13 = Resistor [tolerance=±5% resistance=220 package=THT]
  R14 = Resistor [tolerance=±5% resistance=220 package=THT]
  R15 = Resistor [tolerance=±5% resistance=220 package=THT]
  R16 = Resistor [tolerance=±5% resistance=220 package=THT]
  R17 = Resistor [tolerance=±5% resistance=220 package=THT]
  U1 = PCF8574 [package="DIP16 [THT]"]
  U2 = 74HC595 [package="DIP16 [THT]"]

nets:
  N1: Part1.A4/SDA, U1.SDA
  N2: Part1.A5/SCL, U1.SCL
  N3: Part1.D8, U2.ST_CP
  N4: Part1.D11_PWM/MOSI, U2.DS
  N5: Part1.D12/MISO, U2.SH_CP
  N6: Part1.D2, R15.Pin_1
  VCC: Part1.5V, LED6.anode, LED8.anode, LED19.anode, LED20.anode, LED21.anode, LED22.anode, LED23.anode, LED24.anode, U1.VCC, U2.MR, U2.VCC
  GND: Part1.GND, LED10.cathode, LED18.cathode, LED25.cathode, LED26.cathode, LED27.cathode, LED28.cathode, LED29.cathode, LED30.cathode, LED31.cathode, U1.A0, U1.A1, U1.A3, U1.GND, U2.GND, U2.OE
  N7: LED6.cathode, R1.Pin_0
  N8: LED8.cathode, R14.Pin_0
  N9: LED10.anode, R12.Pin_0
  N10: LED18.anode, R17.Pin_0
  N11: LED19.cathode, R2.Pin_0
  N12: LED20.cathode, R3.Pin_0
  N13: LED21.cathode, R4.Pin_0
  N14: LED22.cathode, R5.Pin_0
  N15: LED23.cathode, R6.Pin_0
  N16: R1.Pin_1, U1.P0
  N17: R2.Pin_1, U1.P1
  N18: R3.Pin_1, U1.P5
  N19: R4.Pin_1, U1.P4
  N20: R5.Pin_1, U1.P3
  N21: R6.Pin_1, U1.P2
  N22: LED24.cathode, R13.Pin_0
  N23: LED25.anode, R9.Pin_0
  N24: LED26.anode, R10.Pin_0
  N25: LED27.anode, R11.Pin_0
  N26: LED28.anode, R8.Pin_0
  N27: LED29.anode, R7.Pin_0
  N28: LED30.anode, R16.Pin_0
  N29: LED31.anode, R15.Pin_0
  N30: R7.Pin_1, U2.Q5
  N31: R8.Pin_1, U2.Q4
  N32: R9.Pin_1, U2.Q3
  N33: R10.Pin_1, U2.Q2
  N34: R11.Pin_1, U2.Q1
  N35: R12.Pin_1, U2.Q0
  N36: R13.Pin_1, U1.P7
  N37: R14.Pin_1, U1.P6
  N38: R16.Pin_1, U2.Q7
  N39: R17.Pin_1, U2.Q6
