# Fritzing sketch id3763_Simple_Buzzer__0 (saved by Fritzing 0.8.5b)
circuit board: 3.15008cm x 1.61437cm
breadboards: 1

parts:
  Q1 = TRANSISTOR_NPN [package=to-92-ammo]
  R1 = Resistor [tolerance=±5% resistance=1k package=THT]
  R2 = Resistor [tolerance=±5% resistance=1k package=THT]
  J1 = female pin header, 1 pin [form="♀ (female)"]
  Buz1 = Piezo Speaker
  J3 = female pin header, 1 pin [form="♀ (female)"]
  J2 = female pin header, 1 pin [form="♀ (female)"]

nets:
  N1: Q1.E, J2.pin1
  N2: Q1.B, R2.Pin_1
  N3: Q1.C, R1.Pin_0, Buz1.pin1
  N4: R1.Pin_1, J1.pin1, Buz1.pin2
  N5: R2.Pin_0, J3.pin1
