# Fritzing sketch id3765_SIMPLE_DYNO_0 (saved by Fritzing 0.8.7b)
breadboards: 1

parts:
  Part1 = Arduino Pro Mini v13
  R1 = Resistor [tolerance=±5% resistance=75 package=THT]
  Q1 = PHOTOTRANSISTOR REFLECTIVE OBJECT SENSOR [part_number=OPB704WZ package=qrb1114-side]
  R2 = Resistor [tolerance=±5% resistance=10k package=THT]

nets:
  5V: Part1.VCC, R1.Pin_0, R2.Pin_0
  N1: Part1.GND, Q1.E, Q1.K
  N2: Part1.D2, Q1.C, R2.Pin_1
  N3: R1.Pin_1, Q1.A
