# Fritzing sketch id3766_Arduino_giardino_02_0 (saved by Fritzing 0.9.0b)
breadboards: 2

parts:
  Componente1 = Arduino Uno (Rev3)
  R1 = Resistor [tolerance=±5% resistance=470 package=THT]
  R2 = Resistor [tolerance=±5% resistance=470 package=THT]
  LCD1 = LCD screen
  S3 = Round Pushbutton
  S4 = Round Pushbutton
  R3 = Rotary Potentiometer (Small) [maximum_resistance=100kΩ package=THT]
  DHT1 = DHT11_Temperature_and_Humitidy_Sensor
  DHT2 = DHT22_Humidity_and_Temperature_Sensor
  R4 = Resistor [tolerance=±5% resistance=1k package=THT]
  DS1307 = DS1307_RTC_Breakout
  J1 = Piezo Speaker
  KY-1 = keyes
  ACS712 = ACS712 Low Current Sensor Board v12
  R5 = Resistor [tolerance=±5% resistance=10k package=THT]
  R6 = Resistor [tolerance=±10% resistance=10k package=THT]
  C1 = Electrolytic Capacitor [capacitance=10µF voltage=10V package="100 mil [THT, electrolytic]"]
  R7 = Resistor [tolerance=±20% resistance=10k package=THT]
  R8 = Resistor [tolerance=±5% resistance=100k package=THT]
  Componente2 = richardbruneau00000
  Componente3 = richardbruneau00000
  Raspberry_Pi_B_rev1 = Raspberry Pi B rev2  # not connected

nets:
  N1: Componente1.A0, ACS712.VO
  GND: Componente1.A1, Componente1.GND, LCD1.VSS, LCD1.R/W, S3.leg0, S4.leg0, R3.leg1, DHT1.connector4, DHT2.connector4, DS1307.connector1, J1.pin1, KY-1.connector2, ACS712.GND, R6.Pin_0, C1.-, Componente2.connector9
  N2: Componente1.A2, Componente2.connector11
  N3: Componente1.A4/SDA, DS1307.connector3
  N4: Componente1.A5/SCL, DS1307.connector4
  N5: Componente1.D8, DHT2.connector2, R4.Pin_1
  N6: Componente1.D9_PWM, KY-1.connector0
  N7: Componente1.D10_PWM/SS, J1.pin2
  N8: Componente1.D11_PWM/MOSI, LCD1.E
  N9: Componente1.D12/MISO, LCD1.RS
  N10: Componente1.D13/SCK, DHT1.connector2
  N11: Componente1.D2, LCD1.DB7
  N12: Componente1.D3_PWM, LCD1.DB6
  N13: Componente1.D4, LCD1.DB5
  N14: Componente1.D5_PWM, LCD1.DB4
  N15: Componente1.D6_PWM, R1.Pin_0, S3.leg1
  N16: Componente1.D7, R2.Pin_0, S4.leg1
  N17: Componente1.3V3, DHT2.connector1, R4.Pin_0, Componente2.connector8
  5V: Componente1.5V, DS1307.connector2, ACS712.5V, R5.Pin_0
  N18: R1.Pin_1, R2.Pin_1, LCD1.VDD, R3.leg2, DHT1.connector1, KY-1.connector1
  N19: LCD1.V0, R3.wiper
  N20: R5.Pin_1, R6.Pin_1, C1.+, R7.Pin_1
  N21: R7.Pin_0, R8.Pin_1
  N22: Componente2.connector12, Componente3.connector8
  N23: Componente2.connector13, Componente3.connector9

notes:
  Solenoid valve
  + DC 24V -
  Phase electric power
  AC 9V
