# Fritzing sketch id3767_FM_Transmitter_0 (saved by Fritzing 0.9.3b)
circuit board: 6.42568cm x 3.61712cm
breadboards: 1

parts:
  +3V = Battery
  Coil = Inductor [package="400 mil [THT]"]
  56pF = Ceramic Capacitor [capacitance=100nF package="100 mil [THT, multilayer]"]
  ANT = Antenna
  47_pF = Ceramic Capacitor [capacitance=100nF package="100 mil [THT, multilayer]"]
  Q1 = NPN-Transistor [package="TO92 [THT]"]
  100K = Resistor [tolerance=±5% resistance=10k package=THT]
  10K = Resistor [tolerance=±5% resistance=220 package=THT]

nets:
  N1: +3V.-, Q1.E, 10K.Pin_0
  N2: +3V.+, Coil.pin_1, 56pF.1, 100K.Pin_1
  N3: Coil.pin_0, 56pF.0, 47_pF.0, Q1.C
  N4: ANT.antenna_lead, 47_pF.1
  N5: 100K.Pin_0, 10K.Pin_1

notes:
  Audio
  +
  -
