# Fritzing sketch id3769_3_Wire_LCD_with_shifter2 (saved by Fritzing 0.6.3b)
breadboards: 1

parts:
  Arduino1 = Arduino [part_number=Howdy]
  RGB_LCD = LCD_screen
  Potentiometer = Rotary Potentiometer (Small) [maximum_resistance=100kΩ]
  74HC595 = 74HC595 [package="DIP16 [THT]"]

nets:
  GND: Arduino1.GND, Arduino1.D5, RGB_LCD.connector0, RGB_LCD.connector4, RGB_LCD.connector16, Potentiometer.leg1, 74HC595.GND, 74HC595.OE
  N1: Arduino1.D8, 74HC595.DS
  N2: Arduino1.D7, 74HC595.SH_CP
  N3: Arduino1.D6, RGB_LCD.connector15
  N4: Arduino1.D4, RGB_LCD.connector5, 74HC595.ST_CP
  N5: Arduino1.D3, RGB_LCD.connector17
  +5V: Arduino1.+5V, RGB_LCD.connector1, RGB_LCD.connector14, Potentiometer.leg2, 74HC595.MR, 74HC595.VCC
  N6: RGB_LCD.connector2, Potentiometer.wiper
  N7: RGB_LCD.connector3, 74HC595.Q2
  N8: RGB_LCD.connector10, 74HC595.Q3
  N9: RGB_LCD.connector11, 74HC595.Q4
  N10: RGB_LCD.connector12, 74HC595.Q5
  N11: RGB_LCD.connector13, 74HC595.Q6
