# Fritzing sketch id3770_IR_Remote_Tester_Schematic_0 (saved by Fritzing 0.9.2b)
breadboards: 1

parts:
  J1 = Infrared Proximity Sensor
  SG1 = Buzzer 12mm [package=buzzer-ccv]
  R1 = Resistor [tolerance=±5% resistance=220 package=THT]
  LED1 = LED - 5mm [color="Red (633nm)" package="5 mm [THT]"]
  C1 = Capacitor Polarized [package=panasonic_h13]
  VCC1 = Battery block 9V

nets:
  N1: J1.Vout, SG1.2, LED1.cathode
  N2: J1.GND, C1.-, VCC1.-
  N3: J1.Vcc, SG1.1, R1.Pin_1, VCC1.+
  N4: R1.Pin_0, LED1.anode, C1.+
