# Fritzing sketch id3771_IR_Remote_Tester_0 (saved by Fritzing 0.9.2b)
circuit board: 8.46667cm x 5.64444cm
breadboards: 1

parts:
  J1 = Infrared Proximity Sensor
  SG1 = Buzzer 12mm [package=buzzer-ccv-kit]
  R1 = Resistor [tolerance=±5% resistance=220 package=THT]
  LED1 = LED - 5mm [color="Red (633nm)" package="5 mm [THT]"]
  VCC1 = Battery block 9V
  C1 = Capacitor Polarized [package=panasonic_c]

nets (from the pcb view):
  N1: J1.Vout, SG1.2, R1.Pin_1, VCC1.-, C1.-
  N2: J1.GND, SG1.1, LED1.cathode
  N3: J1.Vcc, VCC1.+, C1.+
  N4: R1.Pin_0, LED1.anode
