# Fritzing sketch id3772_laser_alarm_0 (saved by Fritzing 0.9.1b)
circuit board: 8.46667cm x 5.64444cm
breadboards: 1

parts:
  R1 = Photocell (LDR) [package=THT]
  R2 = Resistor [tolerance=±5% resistance=10k package=THT]
  Part1 = Arduino Uno (Rev3)
  J1 = Piezo Speaker

nets:
  N1: R1.pin_0, Part1.5V
  N2: R1.pin_1, R2.Pin_0, Part1.A0
  N3: R2.Pin_1, Part1.GND, J1.pin1
  N4: Part1.D12/MISO, J1.pin2
