# Fritzing sketch id3773_led_0 (saved by Fritzing 0.9.3b)
breadboards: 1

parts:
  LED1 = smd LED [color="Red (633nm)" package="1206 [SMD]"]
  LED2 = smd LED [color="Blue (470nm)" package="1206 [SMD]"]
  VCC1 = Battery

nets:
  N1: LED1.cathode, LED2.cathode, VCC1.-
  N2: LED1.anode, LED2.anode, VCC1.+
