# Fritzing sketch id3774_LED_Rodeo_0 (saved by Fritzing 0.7.6b)
breadboards: 1

parts:
  Arduino1 = Arduino
  R4 = Resistor [tolerance=±5% resistance=220 package=THT]
  R5 = Resistor [tolerance=±5% resistance=220 package=THT]
  R6 = Resistor [tolerance=±5% resistance=220 package=THT]
  R7 = Resistor [tolerance=±5% resistance=220 package=THT]
  R8 = Resistor [tolerance=±5% resistance=220 package=THT]
  R9 = Resistor [tolerance=±5% resistance=220 package=THT]
  LED1 = LED - 5mm [color="Green (570nm)" package="5 mm [THT]"]
  LED2 = LED - 5mm [color="Yellow (595nm)" package="5 mm [THT]"]
  LED3 = LED - 5mm [color="Red (633nm)" package="5 mm [THT]"]
  LED4 = LED - 5mm [color="Green (570nm)" package="5 mm [THT]"]
  LED5 = LED - 5mm [color="Yellow (595nm)" package="5 mm [THT]"]
  LED6 = LED - 5mm [color="Red (633nm)" package="5 mm [THT]"]

nets:
  N1: Arduino1.GND, LED1.cathode, LED2.cathode, LED3.cathode, LED4.cathode, LED5.cathode, LED6.cathode
  N2: Arduino1.D11, R5.Pin_0
  N3: Arduino1.D10, R4.Pin_0
  N4: Arduino1.D9, R6.Pin_0
  N5: Arduino1.D6, R7.Pin_0
  N6: Arduino1.D5, R8.Pin_0
  N7: Arduino1.D3, R9.Pin_0
  N8: R4.Pin_1, LED2.anode
  N9: R5.Pin_1, LED1.anode
  N10: R6.Pin_1, LED3.anode
  N11: R7.Pin_1, LED4.anode
  N12: R8.Pin_1, LED5.anode
  N13: R9.Pin_1, LED6.anode
