# Fritzing sketch id3776_Simple_LED_0 (saved by Fritzing 0.9.2b)
breadboards: 1

parts:
  Part1 = Arduino Uno (Rev3)
  LED1 = LED - 5mm [color="Red (633nm)" package="5 mm [THT]"]
  LED2 = LED - 5mm [color="Red (633nm)" package="5 mm [THT]"]
  LED3 = LED - 5mm [color="Red (633nm)" package="5 mm [THT]"]
  LED4 = LED - 5mm [color="Red (633nm)" package="5 mm [THT]"]
  LED5 = LED - 5mm [color="Red (633nm)" package="5 mm [THT]"]
  LED6 = LED - 5mm [color="Red (633nm)" package="5 mm [THT]"]
  R1 = Resistor [tolerance=±5% resistance=220 package=THT]
  R2 = Resistor [tolerance=±5% resistance=220 package=THT]
  R3 = Resistor [tolerance=±5% resistance=220 package=THT]
  R4 = Resistor [tolerance=±5% resistance=220 package=THT]
  R5 = Resistor [tolerance=±5% resistance=220 package=THT]
  R6 = Resistor [tolerance=±5% resistance=220 package=THT]

nets:
  N1: Part1.D2, LED6.cathode
  N2: Part1.D3_PWM, LED5.cathode
  N3: Part1.D4, LED4.cathode
  N4: Part1.D5_PWM, LED3.cathode
  N5: Part1.D6_PWM, LED2.cathode
  N6: Part1.D7, LED1.cathode
  N7: Part1.5V, R1.Pin_0, R2.Pin_0, R3.Pin_0, R4.Pin_0, R5.Pin_0, R6.Pin_0
  N8: LED1.anode, R1.Pin_1
  N9: LED2.anode, R2.Pin_1
  N10: LED3.anode, R3.Pin_1
  N11: LED4.anode, R4.Pin_1
  N12: LED5.anode, R5.Pin_1
  N13: LED6.anode, R6.Pin_1
