# Fritzing sketch id3777_LightShow_0 (saved by Fritzing 0.9.1b)
breadboards: 1

parts:
  Part1 = Arduino Uno (Rev3)
  LED1 = LED - 5mm [color="Red (633nm)" package="5 mm [THT]"]
  LED2 = LED - 5mm [color="Red (633nm)" package="5 mm [THT]"]
  LED3 = LED - 5mm [color="Red (633nm)" package="5 mm [THT]"]
  R1 = Resistor [tolerance=±5% resistance=220 package=THT]
  LED4 = LED - 5mm [color="Red (633nm)" package="5 mm [THT]"]
  R2 = Resistor [tolerance=±5% resistance=220 package=THT]
  R3 = Resistor [tolerance=±5% resistance=220 package=THT]
  R4 = Resistor [tolerance=±5% resistance=220 package=THT]

nets:
  N1: Part1.D9_PWM, R4.Pin_0
  N2: Part1.GND, LED1.cathode, LED2.cathode, LED3.cathode, LED4.cathode
  N3: Part1.D3_PWM, R1.Pin_0
  N4: Part1.D5_PWM, R2.Pin_0
  N5: Part1.D6_PWM, R3.Pin_0
  N6: LED1.anode, R4.Pin_1
  N7: LED2.anode, R3.Pin_1
  N8: LED3.anode, R2.Pin_1
  N9: R1.Pin_1, LED4.anode
