# Fritzing sketch id3778_magnetic_field_detecter_0 (saved by Fritzing 0.9.2b)
circuit board: 6.28798cm x 1.13583cm
breadboards: 1

parts:
  L4 = Inductor [package="400 mil [THT]"]
  L5 = Inductor [package="400 mil [THT]"]
  L6 = Inductor [package="400 mil [THT]"]
  L7 = Inductor [package="400 mil [THT]"]
  L13 = Inductor [package="400 mil [THT]"]
  L14 = Inductor [package="400 mil [THT]"]
  L15 = Inductor [package="400 mil [THT]"]
  L16 = Inductor [package="400 mil [THT]"]
  L17 = Inductor [package="400 mil [THT]"]
  L18 = Inductor [package="400 mil [THT]"]
  L19 = Inductor [package="400 mil [THT]"]
  L20 = Inductor [package="400 mil [THT]"]
  L22 = Inductor [package="400 mil [THT]"]
  L23 = Inductor [package="400 mil [THT]"]
  L24 = Inductor [package="400 mil [THT]"]
  L27 = Inductor [package="400 mil [THT]"]

nets:
  N1: L4.pin_0, L5.pin_0, L6.pin_0, L7.pin_0, L13.pin_1, L14.pin_1, L18.pin_1, L19.pin_1
  N2: L4.pin_1, L5.pin_1, L6.pin_1, L7.pin_1
  N3: L13.pin_0, L14.pin_0, L15.pin_1, L16.pin_1, L17.pin_1, L18.pin_0, L19.pin_0, L20.pin_1
  N4: L15.pin_0, L16.pin_0, L17.pin_0, L20.pin_0, L22.pin_1, L23.pin_1, L24.pin_1, L27.pin_1
  N5: L22.pin_0, L23.pin_0, L24.pin_0, L27.pin_0
