# Fritzing sketch id3779_Mic_2015_06_07_0 (saved by Fritzing 0.9.2b)
breadboards: 1

parts:
  Part1 = Arduino Uno (Rev3)
  MIC1 = Microphone
  LED1 = LED - 5mm [color="Red (633nm)" package="5 mm [THT]"]
  C1 = Electrolytic Capacitor [capacitance=1µF package="100 mil [THT, electrolytic]"]
  R3 = prefix0000
  R4 = prefix0000

nets:
  N1: Part1.A0, C1.-
  N2: Part1.GND, MIC1.pin1, LED1.cathode
  N3: Part1.D3_PWM, R3.connector1
  N4: Part1.5V, R4.connector1
  N5: MIC1.pin2, C1.+, R4.connector0
  N6: LED1.anode, R3.connector0
