# Fritzing sketch id377_arduino2arduino_0 (saved by Fritzing 0.9.2b)

parts:
  Parte1 = Arduino Uno (Rev3)
  Parte2 = Arduino Uno (Rev3)

nets:
  N1: Parte1.D11_PWM/MOSI, Parte2.D12/MISO
  N2: Parte1.D12/MISO, Parte2.D11_PWM/MOSI
  GND: Parte1.GND, Parte2.GND
