# Fritzing sketch id3780_SimpleMotor_0 (saved by Fritzing 0.8.5b)
perfboards: 1

parts:
  M1 = DC Motor
  D1 = Rectifier Diode [part_number=1N4001 package="300 mil [THT]"]
  VCC1 = Battery block 9V
  U1 = Optocoupler [package=THT]
  R1 = Resistor [tolerance=±5% resistance=10k package=THT]
  R2 = Resistor [tolerance=±5% resistance=220 package=THT]
  Q1 = Basic FET N-Channel [package="TO220 [THT]"]

nets:
  N1: M1.pin_1, D1.anode, Q1.drain
  N2: M1.pin_2, D1.cathode, VCC1.+, U1.Pin_5
  N3: VCC1.-, R1.Pin_1, Q1.source
  mc out: U1.Pin_1
  N4: U1.Pin_2, R2.Pin_0
  N5: U1.Pin_4, R1.Pin_0, Q1.gate
  mc low: R2.Pin_1
