# Fritzing sketch id3782_Solar_Battery_Charger_1_0 (saved by Fritzing 0.9.2b)
breadboards: 1

parts:
  Componente1 = Intel Galileo Gen2
  D1 = SOLAR-IXYS [package=solarbit-12x1]
  R1 = Resistor [tolerance=±5% resistance=10k package="0402 [SMD]"]
  R2 = Resistor [tolerance=±5% resistance=10k package="0402 [SMD]"]
  VCC1 = Battery
  D3 = Rectifier Diode [part_number=1N4001 package="300 mil [THT]"]
  U1 = RELAY [package=relay-g5q]
  R3 = Resistor [tolerance=±5% resistance=10k package="0402 [SMD]"]
  R4 = Resistor [tolerance=±5% resistance=10k package="0402 [SMD]"]

nets:
  N1: Componente1.A0, R1.Pin_1, R2.Pin_0
  N2: Componente1.A1, R3.Pin_0, R4.Pin_1
  N3: Componente1.D4, U1.COIL1
  N4: Componente1.GND, D1.A, R2.Pin_1, VCC1.-, R4.Pin_0
  N5: D1.C, R3.Pin_1
  N6: R1.Pin_0, VCC1.+, D3.anode
  N7: D3.cathode, U1.MAIN

notes:
  Here we are using a relay shield . If you want to use a discrete relay, you will need to use a transistor.
  The ground of everything needs to be connected. Otherwise it won't work. However, I know there are some restriction here that might apply.
