# Fritzing sketch id3783_Lueftermann_FanControlV1.0_0 (saved by Fritzing 0.7.4b)
breadboards: 1

parts:
  Optokuppler = TLP621 [part_number=PC817 package=THT]
  R1 = Resistor [tolerance=±5% resistance=1k package=THT]
  Fuse1 = Fuse with Handler [part_number=Htc-15m]
  Vin_12V = Screw terminal - 2 pins [package=THT]
  R2 = Resistor [tolerance=±5% resistance=1k package=THT]
  LED1 = LED - 3mm [color="Yellow (595nm)" package="3 mm [THT]"]
  Arduino1 = Arduino

nets:
  N1: Optokuppler.Pin_1, R1.Pin_0
  N2: Optokuppler.Pin_2, Optokuppler.Pin_3, Vin_12V.pin1, Arduino1.GND
  N3: Optokuppler.Pin_4, LED1.cathode
  N4: R1.Pin_1, Arduino1.D3
  N5: Fuse1.Connector1, R2.Pin_0, Arduino1.VIN
  N6: Fuse1.Connector2, Vin_12V.pin2
  N7: R2.Pin_1, LED1.anode
