# Fritzing sketch id3784_pi_LED2_0 (saved by Fritzing 0.9.2b)
circuit board: 8.46667cm x 5.64444cm
breadboards: 1

parts:
  Raspberry_Pi1 = Raspberry Pi B+
  LED2 = LED - 5mm [color="Red (633nm)" package="5 mm [THT]"]
  LED3 = LED - 5mm [color="Red (633nm)" package="5 mm [THT]"]
  R1 = Resistor [tolerance=±5% resistance=220 package=THT]
  R2 = Resistor [tolerance=±5% resistance=220 package=THT]
  R3 = Resistor [tolerance=±5% resistance=220 package=THT]
  LED1 = LED - 5mm [color="Red (633nm)" package="5 mm [THT]"]

nets:
  N1: Raspberry_Pi1.GND, LED2.cathode, LED3.cathode, LED1.cathode
  N2: Raspberry_Pi1.GPIO17, R1.Pin_0
  N3: Raspberry_Pi1.GPIO27, R2.Pin_0
  N4: Raspberry_Pi1.GPIO22, R3.Pin_0
  N5: LED2.anode, R2.Pin_1
  N6: LED3.anode, R3.Pin_1
  N7: R1.Pin_1, LED1.anode
