# Fritzing sketch id3785_rpicontrolscheme_0 (saved by Fritzing 0.9.3b)
circuit board: 8.46667cm x 5.64444cm
breadboards: 1

parts:
  Raspberry_Pi_1 = Raspberry Pi 3 [part_number=RPI-3-V1.2]
  R1 = Resistor [tolerance=±5% resistance=1k package="0603 [SMD]"]
  Q1 = NPN-Transistor [package="TO92 [THT]"]
  U1 = RELAY-2 [package=relay-g5v]
  VCC1 = Battery
  LED1 = LED - 5mm [color="Red (633nm)" package="5 mm [THT]"]
  R2 = Resistor [tolerance=±5% resistance=220 package=THT]

nets:
  N1: Raspberry_Pi_1.GPIO17, R1.Pin_1
  N2: Raspberry_Pi_1.GND, Q1.E
  N3: Raspberry_Pi_1.5V, U1.2
  N4: R1.Pin_0, Q1.B
  N5: Q1.C, U1.9
  N6: U1.6, VCC1.-
  N7: U1.10, R2.Pin_0
  N8: VCC1.+, LED1.anode
  N9: LED1.cathode, R2.Pin_1
