# Fritzing sketch id3786_RGBLed_0 (saved by Fritzing 0.7.11b)
breadboards: 1

parts:
  Arduino1 = Arduino
  LED1 = RGB LED (com. anode, rbg) [package="5 mm [THT]"]
  R1 = Resistor [tolerance=±5% resistance=3.3k package=THT]
  R2 = Resistor [tolerance=±5% resistance=3.3k package=THT]
  R3 = Resistor [tolerance=±5% resistance=3.3k package=THT]

nets:
  N1: Arduino1.+5V, LED1.common_anode
  N2: LED1.red_cathode, R1.Pin_0
  N3: LED1.blue_cathode, R2.Pin_0
  N4: LED1.green_cathode, R3.Pin_0

notes:
  Arduino Uno + RGB LED
  Derek Erb - 22/02/2013
  about.me/derekerb
  derek.erb@gmail.com
  LED Pins
  Red - Anode - Blue - Green
