# Fritzing sketch id3787_ardumoto_0 (saved by Fritzing 0.7.0b)

parts:
  Part1 = Arduino Motor Shield
  M1 = DC Motor
  M2 = DC Motor
  VCC1 = 4 x AAA Battery Mount  # not connected
  S1 = Toggle Switch [package=THT]
  Part2 = Bluetooth Mate Silver

nets:
  N1: Part1.VIN, S1.L2
  N2: Part1.OUT3, M1.pin_2
  N3: Part1.OUT4, M1.pin_1
  N4: Part1.OUT2, M2.pin_2
  N5: Part1.OUT1, M2.pin_1
  5V: Part1.5V, Part2.VCC
  GND: Part1.GND, Part2.GND
  N6: Part1.RX, Part2.TX_5V
  N7: Part1.TX, Part2.RX_5V
