# Fritzing sketch id3788_SevenSegmentArduino1_0 (saved by Fritzing 0.8.5b)
circuit board: 8.60961cm x 8.37428cm
breadboards: 1

parts:
  Part1 = Arduino Uno (Rev3)
  7_Segment1 = 7 Segment Display
  R1 = Resistor [tolerance=±5% resistance=680 package=THT]

nets:
  N1: Part1.D8, 7_Segment1.Segment_E
  N2: Part1.D9_PWM, 7_Segment1.Segment_F
  N3: Part1.D10_PWM/SS, 7_Segment1.Segment_G
  N4: Part1.D11_PWM/MOSI, 7_Segment1.Segment_B
  N5: Part1.D12/MISO, 7_Segment1.Segment_A
  GND: Part1.GND
  N6: Part1.D6_PWM, 7_Segment1.Segment_C
  N7: Part1.D7, 7_Segment1.Segment_D
  5V: Part1.5V, R1.Pin_0
  N8: 7_Segment1.common_anode, R1.Pin_1
