# Fritzing sketch id3789_Simple_Shift_Register_0 (saved by Fritzing 0.9.1b)
breadboards: 1

parts:
  U1 = 74HC595 [package="DIP16 [THT]"]
  Part1 = Arduino Uno (Rev3)

nets:
  GND: U1.GND, U1.Q0, Part1.GND
  N1: U1.SH_CP, Part1.D4
  N2: U1.ST_CP, Part1.D3_PWM
  N3: U1.DS, Part1.D5_PWM
  VCC: U1.VCC, Part1.5V
