# Fritzing sketch id3790_thermoter_0 (saved by Fritzing 0.9.2b)
breadboards: 1

parts:
  Part1 = Arduino Uno (Rev3)
  R1 = Resistor [tolerance=±5% resistance=220 package=THT]
  R2 = Resistor [tolerance=±5% resistance=220 package=THT]
  R3 = Resistor [tolerance=±5% resistance=220 package=THT]
  LED1 = LED - 5mm [color="Red (633nm)" package="5 mm [THT]"]
  LED2 = LED - 5mm [color="Red (633nm)" package="5 mm [THT]"]
  LED3 = LED - 5mm [color="Red (633nm)" package="5 mm [THT]"]
  T1 = LM35 Temperature Sensor [package="TO92 [THT]"]

nets:
  N1: Part1.A0, T1.Vout
  N2: Part1.D2, LED1.anode
  N3: Part1.D3_PWM, LED2.anode
  N4: Part1.D4, LED3.anode
  N5: Part1.5V, T1.+Vs
  GND: Part1.GND, R1.Pin_1, R2.Pin_0, R3.Pin_0, T1.GND
  N6: R1.Pin_0, LED3.cathode
  N7: R2.Pin_1, LED2.cathode
  N8: R3.Pin_1, LED1.cathode
