# Fritzing sketch id3791_digital_torch_0 (saved by Fritzing 0.9.2b)
breadboards: 1

parts:
  S1 = Momentary Switch [package=ksa_sealed_tac_switch]
  R2 = Resistor [tolerance=±5% resistance=220 package=THT]
  LED1 = LED - 5mm [color="Red (633nm)" package="5 mm [THT]"]
  Εξάρτημα1 = Arduino Uno (Rev3)
  R1 = Resistor [tolerance=±5% resistance=10k package=THT]
  S4 = Momentary Switch [package=ksa_sealed_tac_switch]  # not connected

nets:
  N1: S1.1, Εξάρτημα1.D2, R1.Pin_0
  N2: S1.4, Εξάρτημα1.5V
  N3: R2.Pin_0, LED1.anode
  N4: R2.Pin_1, Εξάρτημα1.D13/SCK
  N5: LED1.cathode, Εξάρτημα1.GND, R1.Pin_1

notes:
  +5 Volts
  [GND]
  κανονικοί ακροδέκτες διακόπτη
