# Fritzing sketch id3792_USB_LED_0 (saved by Fritzing 0.7.0b)
breadboards: 1

parts:
  USB = USB connector [package=THT]
  XTAL1 = Crystal
  C1 = Ceramic Capacitor [capacitance=10pF package="100 mil [THT, multilayer]"]
  C2 = Ceramic Capacitor [capacitance=10pF package="100 mil [THT, multilayer]"]
  LED1 = LED - 5mm [color="Red (633nm)" package="5 mm [THT]"]
  R1 = Resistor [tolerance=±5% resistance=680 package=THT]
  R2 = Resistor [tolerance=±5% resistance=4.7k package=THT]
  D1 = Rectifier Diode [part_number=1N4001 package="300 mil [THT]"]
  D2 = Rectifier Diode [part_number=1N4001 package="300 mil [THT]"]
  D3 = Rectifier Diode [part_number=1N4001 package="300 mil [THT]"]
  R3 = Resistor [tolerance=±5% resistance=68 package=THT]
  R4 = Resistor [tolerance=±5% resistance=68 package=THT]
  R5 = Resistor [tolerance=±5% resistance=1.5k package=THT]
  R6 = Resistor [tolerance=±5% resistance=1M package=THT]
  AtTiny2313-20PU = IC, DIP package, 20 pins [chip_label=AtTiny2313-20PU spacing=300mil]
  ISP_Header = Generic_shrouded_header___6_pins [form="♂ (shrouded male)"]

nets:
  N1: USB.5V, D1.anode, ISP_Header.connector5
  N2: USB.d-, R4.Pin_0, R5.Pin_0
  N3: USB.d+, R3.Pin_0, R6.Pin_0
  N4: USB.GND, USB.chassis5, USB.chassis6, C1.1, C2.0, AtTiny2313-20PU.pin10, ISP_Header.connector3
  N5: XTAL1.connector0, C1.0, AtTiny2313-20PU.pin5
  N6: XTAL1.connector1, C2.1, AtTiny2313-20PU.pin4
  N7: LED1.cathode, R1.Pin_0
  N8: LED1.anode, AtTiny2313-20PU.pin12
  N9: R1.Pin_1, R2.Pin_1, D3.cathode, R5.Pin_1, R6.Pin_1, AtTiny2313-20PU.pin20
  N10: R2.Pin_0, AtTiny2313-20PU.pin1, ISP_Header.connector2
  N11: D1.cathode, D2.anode
  N12: D2.cathode, D3.anode
  N13: R3.Pin_1, AtTiny2313-20PU.pin6
  N14: R4.Pin_1, AtTiny2313-20PU.pin7
  N15: AtTiny2313-20PU.pin17, ISP_Header.connector4
  N16: AtTiny2313-20PU.pin18, ISP_Header.connector0
  N17: AtTiny2313-20PU.pin19, ISP_Header.connector1
