# Fritzing sketch id3793_schematic_0 (saved by Fritzing 0.9.0b)
breadboards: 1

parts:
  LED1 = LED - 5mm [color="Red (633nm)" package="5 mm [THT]"]
  R3 = Temperature Sensor (Thermistor) [thermistor_type=NTC package=THT]
  IC1 = IC, DIP package, 8 pins [chip_label=TL072]
  VCC1 = Battery block 9V
  R1 = Trimmer Potentiometer [maximum_resistance=10kΩ package=THT]
  R2 = Resistor [tolerance=±5% resistance=330 package=THT]
  R4 = Resistor [tolerance=±5% resistance=47k package=THT]
  R5 = Trimmer Potentiometer [maximum_resistance=10kΩ package=THT]
  R6 = Resistor [tolerance=±5% resistance=330 package=THT]
  LED2 = LED - 5mm [color="Red (633nm)" package="5 mm [THT]"]

nets:
  N1: LED1.cathode, R3.pin_1, IC1.pin8, VCC1.+, R1.leg1, R5.leg2
  N2: LED1.anode, R2.Pin_0
  N3: R3.pin_0, IC1.pin2, IC1.pin6, R4.Pin_1
  N4: IC1.pin1, R2.Pin_1
  N5: IC1.pin3, R1.wiper
  N6: IC1.pin4, VCC1.-, R1.leg2, R4.Pin_0, R5.leg1, LED2.cathode
  N7: IC1.pin5, R5.wiper
  N8: IC1.pin7, R6.Pin_1
  N9: R6.Pin_0, LED2.anode
