# Fritzing sketch id3795_simplebot_0 (saved by Fritzing 0.9.1b)

parts:
  J1 = Basic Servo
  J2 = Basic Servo
  Part1 = Arduino Nano (Rev3.0) (ICSP)
  Part2 = Bluetooth HC-05 Macho
  BAT1 = Battery Holders [package=battery-aaa]
  BAT2 = Battery Holders [package=battery-aaa]
  BAT3 = Battery Holders [package=battery-aaa]
  BAT4 = Battery Holders [package=battery-aaa]
  BAT5 = Battery Holders [package=battery-aaa]
  BAT6 = Battery Holders [package=battery-aaa]

nets:
  GND: J1.gnd, J2.gnd, Part1.GND, Part2.GND, BAT1.+
  VCC: J1.vcc, J2.vcc, Part1.VIN, BAT6.-
  N1: J1.pulse, Part1.D12/MISO
  N2: J2.pulse, Part1.D11/MOSI
  N3: Part1.D1/TX, Part2.RXD
  N4: Part1.D0/RX, Part2.TXD
  5V: Part1.5V, Part2.VCC
  N5: BAT1.-, BAT2.+
  N6: BAT2.-, BAT3.+
  N7: BAT3.-, BAT4.+
  N8: BAT4.-, BAT5.+
