# Fritzing sketch id3796_servos_0 (saved by Fritzing 0.9.1b)

parts:
  J1 = Basic Servo
  J2 = Basic Servo
  Part1 = Arduino Nano (Rev3.0) (ICSP)
  BAT1 = Battery Holders [package=battery-aaa]
  BAT2 = Battery Holders [package=battery-aaa]
  BAT3 = Battery Holders [package=battery-aaa]
  BAT4 = Battery Holders [package=battery-aaa]
  BAT5 = Battery Holders [package=battery-aaa]
  BAT6 = Battery Holders [package=battery-aaa]

nets:
  GND: J1.gnd, J2.gnd, Part1.GND, BAT1.+
  VCC: J1.vcc, J2.vcc, Part1.VIN, BAT6.-
  N1: J1.pulse, Part1.D12/MISO
  N2: J2.pulse, Part1.D11/MOSI
  N3: BAT1.-, BAT2.+
  N4: BAT2.-, BAT3.+
  N5: BAT3.-, BAT4.+
  N6: BAT4.-, BAT5.+
