# Fritzing sketch id3798_simpleduino_mk3_r1_0 (saved by Fritzing 0.9.0b)
circuit board: 7.06277cm x 3.10295cm
breadboards: 1

parts:
  ATmega = atmega328 [package=dip]
  AREF_A0-5 = male pin header, 7 pins [form="♂ (male)"]
  D4-D0 = male pin header, 5 pins [form="♂ (male)"]
  5v_in = male pin header, 1 pin [form="♂ (male)"]
  -_+ = male pin header, 1 pin [form="♂ (male)"]
  16MHz = Crystal [frequency="16 Mhz" package=THT]
  C3 = Capacitor [package=cap-pth-small2]
  C4 = Capacitor [package=cap-pth-small2]
  R1 = Resistor [tolerance=±5% resistance=220 package=THT]
  R2 = Resistor [tolerance=±5% resistance=220 package=THT]
  LED13 = LED - 5mm [color="Red (633nm)" package="5 mm [THT]"]
  Reset = Momentary Switch [package=ksa_sealed_tac_switch]
  5v = male pin header, 4 pins [form="♂ (male)"]
  GND = male pin header, 4 pins [form="♂ (male)"]
  D5-13 = male pin header, 9 pins [form="♂ (male)"]
  RST = female pin header, 1 pin [form="♀ (female)"]
  L7805 = Voltage Regulator - 3.3V [package="TO220 [THT]"]
  -_+_2 = female pin header, 2 pins [form="♀ (female)"]
  C1 = Capacitor Polarized [package=cpol-radial-10uf-25v]
  C2 = Capacitor Polarized [package=cpol-radial-10uf-25v]

nets:
  N1: ATmega.RESET, R1.Pin_0, Reset.1, RST.pin1
  N2: ATmega.D0_(RX), D4-D0.pin1
  N3: ATmega.D1_(TX), D4-D0.pin2
  N4: ATmega.D2, D4-D0.pin3
  N5: ATmega.D3_(PWM), D4-D0.pin4
  N6: ATmega.D4, D4-D0.pin5
  N7: ATmega.VCC, ATmega.AVCC, 5v_in.pin1, R1.Pin_1, R2.Pin_0, 5v.pin1, 5v.pin2, 5v.pin3, 5v.pin4, L7805.output_voltage, C2.+
  GND: ATmega.GND, -_+.pin1, C3.2, C4.1, Reset.4, GND.pin1, GND.pin2, GND.pin3, GND.pin4, L7805.GND, -_+_2.pin1, C1.-, C2.-
  N8: ATmega.XLAT1, 16MHz.pin_0, C3.1
  N9: ATmega.XLAT2, 16MHz.pin_1, C4.2
  N10: ATmega.D5_(PWM), D5-13.pin9
  N11: ATmega.D6_(PWM), D5-13.pin8
  N12: ATmega.D7, D5-13.pin7
  N13: ATmega.D8, D5-13.pin6
  N14: ATmega.D9_(PWM), D5-13.pin5
  N15: ATmega.D10_(PWM), D5-13.pin4
  N16: ATmega.D11_(PWM), D5-13.pin3
  N17: ATmega.D12, D5-13.pin2
  N18: ATmega.D13, LED13.cathode, D5-13.pin1
  N19: ATmega.AREF, AREF_A0-5.pin7
  N20: ATmega.A0, AREF_A0-5.pin6
  N21: ATmega.A1, AREF_A0-5.pin5
  N22: ATmega.A2, AREF_A0-5.pin4
  N23: ATmega.A3, AREF_A0-5.pin3
  N24: ATmega.A4, AREF_A0-5.pin2
  N25: ATmega.A5, AREF_A0-5.pin1
  N26: R2.Pin_1, LED13.anode
  N27: L7805.input_voltage, -_+_2.pin2, C1.+

notes:
  SimpleDuino
  MKIII
  7.5-25v
