# Fritzing sketch id3799_simpleduino_r1_0 (saved by Fritzing 0.9.0b)
circuit board: 8.76426cm x 5.4353cm
breadboards: 1

parts:
  1_ATmega = atmega328 [package=dip]
  A0-5_AREF = male pin header, 7 pins [form="♂ (male)"]
  D0-4 = male pin header, 5 pins [form="♂ (male)"]
  5v_in = male pin header, 1 pin [form="♂ (male)"]
  GND = male pin header, 1 pin [form="♂ (male)"]
  16MHz = Crystal [frequency="16 Mhz" package=THT]
  22pF = Capacitor [package=cap-pth-small2]
  22pF_2 = Capacitor [package=cap-pth-small2]
  10kΩ = Resistor [tolerance=±5% resistance=220 package=THT]
  220Ω = Resistor [tolerance=±5% resistance=220 package=THT]
  LED13 = LED - 5mm [color="Red (633nm)" package="5 mm [THT]"]
  Reset = Momentary Switch [package=ksa_sealed_tac_switch]
  5v = male pin header, 4 pins [form="♂ (male)"]
  GND_2 = male pin header, 4 pins [form="♂ (male)"]
  D5-13 = male pin header, 9 pins [form="♂ (male)"]
  MOSI_RST = male pin header, 2 pins [form="♂ (male)"]
  MISO_SCK = male pin header, 2 pins [form="♂ (male)"]
  J3 = female pin header, 1 pin [form="♀ (female)"]
  J4 = female pin header, 1 pin [form="♀ (female)"]

nets:
  N1: 1_ATmega.RESET, 10kΩ.Pin_0, Reset.3, J3.pin1
  N2: 1_ATmega.D0_(RX), D0-4.pin1
  N3: 1_ATmega.D1_(TX), D0-4.pin2
  N4: 1_ATmega.D2, D0-4.pin3
  N5: 1_ATmega.D3_(PWM), D0-4.pin4
  N6: 1_ATmega.D4, D0-4.pin5
  N7: 1_ATmega.VCC, 1_ATmega.AVCC, 5v_in.pin1, 10kΩ.Pin_1, 220Ω.Pin_0, 5v.pin1, 5v.pin2, 5v.pin3, 5v.pin4
  N8: 1_ATmega.GND, GND.pin1, 22pF.2, 22pF_2.1, Reset.2, GND_2.pin1, GND_2.pin2, GND_2.pin3, GND_2.pin4
  N9: 1_ATmega.XLAT1, 16MHz.pin_0, 22pF.1
  N10: 1_ATmega.XLAT2, 16MHz.pin_1, 22pF_2.2
  N11: 1_ATmega.D5_(PWM), D5-13.pin9
  N12: 1_ATmega.D6_(PWM), D5-13.pin8
  N13: 1_ATmega.D7, D5-13.pin7
  N14: 1_ATmega.D8, D5-13.pin6
  N15: 1_ATmega.D9_(PWM), D5-13.pin5
  N16: 1_ATmega.D10_(PWM), D5-13.pin4
  N17: 1_ATmega.D11_(PWM), D5-13.pin3, MOSI_RST.pin2
  N18: 1_ATmega.D12, D5-13.pin2, MOSI_RST.pin1
  N19: 1_ATmega.D13, LED13.cathode, D5-13.pin1, MISO_SCK.pin1
  N20: 1_ATmega.AREF, A0-5_AREF.pin7
  N21: 1_ATmega.A0, A0-5_AREF.pin6
  N22: 1_ATmega.A1, A0-5_AREF.pin5
  N23: 1_ATmega.A2, A0-5_AREF.pin4
  N24: 1_ATmega.A3, A0-5_AREF.pin3
  N25: 1_ATmega.A4, A0-5_AREF.pin2
  N26: 1_ATmega.A5, A0-5_AREF.pin1
  N27: 220Ω.Pin_1, LED13.anode
  N28: MISO_SCK.pin2, J4.pin1

notes:
  SimpleDuino
