# Fritzing sketch id379_Arduino_3_minutes_timer_0 (saved by Fritzing 0.9.3b)
perfboards: 1

parts:
  Part1 = Arduino Uno (Rev3)
  LED1 = smd LED [color="Red (633nm)" package="1206 [SMD]"]
  LED2 = smd LED [color="Yellow (585nm)" package="1206 [SMD]"]
  LED3 = smd LED [color="Green (565nm)" package="1206 [SMD]"]
  R1 = Resistor [tolerance=±5% resistance=220 package="0603 [SMD]"]
  R2 = Resistor [tolerance=±5% resistance=220 package="0603 [SMD]"]
  R3 = Resistor [tolerance=±5% resistance=220 package="0603 [SMD]"]
  S1 = Round Pushbutton
  BAT1 = BC9VPC [package=bc9vpc]
  7_Segment2 = 7 Segment Display
  7_Segment1 = 7 Segment Display

nets:
  N1: Part1.D8, 7_Segment2.Segment_F, 7_Segment1.Segment_F
  N2: Part1.D9_PWM, 7_Segment2.Segment_G, 7_Segment1.Segment_G
  N3: Part1.D10_PWM/SS, 7_Segment2.Segment_C, 7_Segment1.Segment_C
  N4: Part1.D11_PWM/MOSI, 7_Segment1.common_cathode
  N5: Part1.D12/MISO, 7_Segment2.Segment_D, 7_Segment1.Segment_D
  N6: Part1.D13/SCK, 7_Segment2.Segment_E, 7_Segment1.Segment_E
  N7: Part1.D1/TX, S1.leg0
  N8: Part1.D2, LED1.anode
  N9: Part1.D3_PWM, LED2.anode
  N10: Part1.D4, LED3.anode
  N11: Part1.D5_PWM, 7_Segment2.Segment_B, 7_Segment1.Segment_B
  N12: Part1.D6_PWM, 7_Segment2.Segment_A, 7_Segment1.Segment_A
  N13: Part1.D7, 7_Segment2.common_cathode
  N14: Part1.GND, S1.leg1
  N15: Part1.VIN, BAT1.V+
  N16: LED1.cathode, R1.Pin_0
  N17: LED2.cathode, R2.Pin_0
  N18: LED3.cathode, R3.Pin_1
  N19: R1.Pin_1, R2.Pin_1, R3.Pin_0, BAT1.V-
