# Fritzing sketch id3800_semaforo_simples_0 (saved by Fritzing 0.8.6b)
circuit board: 7.86536cm x 6.12764cm
breadboards: 1

parts:
  Semaforo = Arduino Uno (Rev3)
  R1 = Resistor [tolerance=±5% resistance=220 package=THT]
  R2 = Resistor [tolerance=±5% resistance=220 package=THT]
  R3 = Resistor [tolerance=±5% resistance=220 package=THT]
  LED1 = LED - 5mm [color="Red (633nm)" package="5 mm [THT]"]
  LED3 = LED - 5mm [color="Green (555nm)" package="5 mm [THT]"]
  LED2 = LED - 5mm [color="Yellow (595nm)" package="5 mm [THT]"]

nets:
  N1: Semaforo.D8, LED3.anode
  N2: Semaforo.D9_PWM, LED2.anode
  N3: Semaforo.D10_PWM/SS, LED1.anode
  N4: Semaforo.GND, R1.Pin_1, R2.Pin_1, R3.Pin_1
  N5: R1.Pin_0, LED1.cathode
  N6: R2.Pin_0, LED2.cathode
  N7: R3.Pin_0, LED3.cathode

notes:
  Semáforo Simples
  Made by Silvio
