# Fritzing sketch id3801_MIDI_Keyboard_0 (saved by Fritzing 0.8.3b)
circuit board: 19.05cm x 7.25119cm
breadboards: 2

parts:
  D6 = Pushbutton [package="[THT]"]
  D8 = Pushbutton [package="[THT]"]
  D7 = Pushbutton [package="[THT]"]
  D9 = Pushbutton [package="[THT]"]
  D10 = Pushbutton [package="[THT]"]
  D11 = Pushbutton [package="[THT]"]
  D12 = Pushbutton [package="[THT]"]
  D13 = Pushbutton [package="[THT]"]
  D14_(A0) = Pushbutton [package="[THT]"]
  D15_(A1) = Pushbutton [package="[THT]"]
  D16_(A2) = Pushbutton [package="[THT]"]
  D17_(A3) = Pushbutton [package="[THT]"]
  D5 = Pushbutton [package="[THT]"]
  D4 = Pushbutton [package="[THT]"]
  D3 = Pushbutton [package="[THT]"]
  D2 = Pushbutton [package="[THT]"]
  ATMEGA328P = atmega168 [package=dip]
  DIN5 = DIN-5 jack (MIDI) [package=THT]
  XTAL(16mhz) = Crystal [frequency="16 Mhz" package=THT]
  22pF = Ceramic Capacitor [capacitance=10pF package="100 mil [THT, multilayer]"]
  22pF_2 = Ceramic Capacitor [capacitance=10pF package="100 mil [THT, multilayer]"]
  J1 = male pin header, 6 pins [form="♂ (male)"]
  7805 = Voltage Regulator - 5V [package="TO220 [THT]"]
  EXT_/_USB = Toggle Switch [package=THT]
  10uf = Electrolytic Capacitor [capacitance=1µF package="100 mil [THT, electrolytic]"]
  10uf_2 = Electrolytic Capacitor [capacitance=1µF package="100 mil [THT, electrolytic]"]
  Power_plug1 = Power plug
  1n4007 = Rectifier Diode [part_number=1N4001 package="300 mil [THT]"]
  A4 = Rotary Potentiometer (Small)
  A5 = Rotary Potentiometer (Small)
  220ohm = Resistor [tolerance=±5% resistance=220 package=THT]
  10K = Resistor [tolerance=±5% resistance=10k package=THT]
  0_1uF = Ceramic Capacitor [capacitance=100nF voltage=16V package="200 mil [THT, multilayer]"]

nets:
  GND: D6.Pin_1, D6.Pin_2, D8.Pin_1, D8.Pin_2, D7.Pin_1, D7.Pin_2, D9.Pin_1, D9.Pin_2, D10.Pin_1, D10.Pin_2, D11.Pin_1, D11.Pin_2, D12.Pin_1, D12.Pin_2, D13.Pin_1, D13.Pin_2, D14_(A0).Pin_1, D14_(A0).Pin_2, D15_(A1).Pin_1, D15_(A1).Pin_2, D16_(A2).Pin_1, D16_(A2).Pin_2, D17_(A3).Pin_1, D17_(A3).Pin_2, D5.Pin_1, D5.Pin_2, D4.Pin_1, D4.Pin_2, D3.Pin_1, D3.Pin_2, D2.Pin_1, D2.Pin_2, ATMEGA328P.GND, DIN5.2, 22pF.1, 22pF_2.0, J1.pin6, 7805.GND, 10uf.-, 10uf_2.-, Power_plug1.GND, A4.leg1, A5.leg1
  N1: D6.Pin_3, D6.Pin_4, ATMEGA328P.D6_(PWM)
  N2: D8.Pin_3, D8.Pin_4, ATMEGA328P.D8
  N3: D7.Pin_3, D7.Pin_4, ATMEGA328P.D7
  N4: D9.Pin_3, D9.Pin_4, ATMEGA328P.D9_(PWM)
  N5: D10.Pin_3, D10.Pin_4, ATMEGA328P.D10_(PWM)
  N6: D11.Pin_3, D11.Pin_4, ATMEGA328P.D11_(PWM)
  N7: D12.Pin_3, D12.Pin_4, ATMEGA328P.D12
  N8: D13.Pin_3, D13.Pin_4, ATMEGA328P.D13
  N9: D14_(A0).Pin_3, D14_(A0).Pin_4, ATMEGA328P.A0
  N10: D15_(A1).Pin_3, D15_(A1).Pin_4, ATMEGA328P.A1
  N11: D16_(A2).Pin_3, D16_(A2).Pin_4, ATMEGA328P.A2
  N12: D17_(A3).Pin_3, D17_(A3).Pin_4, ATMEGA328P.A3
  N13: D5.Pin_3, D5.Pin_4, ATMEGA328P.D5_(PWM)
  N14: D4.Pin_3, D4.Pin_4, ATMEGA328P.D4
  N15: D3.Pin_3, D3.Pin_4, ATMEGA328P.D3_(PWM)
  N16: D2.Pin_3, D2.Pin_4, ATMEGA328P.D2
  N17: ATMEGA328P.RESET, 10K.Pin_0, 0_1uF.0
  N18: ATMEGA328P.D0_(RX), J1.pin3
  N19: ATMEGA328P.D1_(TX), DIN5.5, J1.pin2
  N20: ATMEGA328P.VCC, ATMEGA328P.AVCC, ATMEGA328P.AREF, EXT_/_USB.COM, A4.leg2, A5.leg2, 220ohm.Pin_1, 10K.Pin_1
  N21: ATMEGA328P.XLAT1, XTAL(16mhz).pin_1, 22pF_2.1
  N22: ATMEGA328P.XLAT2, XTAL(16mhz).pin_0, 22pF.0
  N23: ATMEGA328P.A4, A5.wiper
  N24: ATMEGA328P.A5, A4.wiper
  N25: DIN5.4, 220ohm.Pin_0
  N26: J1.pin1, 0_1uF.1
  N27: J1.pin4, EXT_/_USB.L1
  N28: 7805.input_voltage, 10uf_2.+, 1n4007.cathode
  N29: 7805.output_voltage, EXT_/_USB.L2, 10uf.+
  N30: Power_plug1.VCC, 1n4007.anode

notes:
  LABORATORIO
  DE
  JUGUETE
  GND
  5V
  RX
  TX
  RST
  SIMPLEST MIDI KEYBOARD
  laboratoriodejuguete.com
