# Fritzing sketch id3802_sensing_buggy_Sketch_2_0 (saved by Fritzing 0.9.2b)
breadboards: 1

parts:
  S1 = Toggle Switch [package=THT]
  M1 = DC Motor
  M2 = DC Motor
  VCC1 = Battery
  S2 = Pushbutton [package=THT]
  S3 = Pushbutton [package=THT]

nets:
  N1: S1.COM, M1.pin_2, M2.pin_1, VCC1.+, S2.leg0, S3.leg1
  N2: S1.L2, VCC1.-
  N3: M1.pin_1, S2.leg1
  N4: M2.pin_2, S3.leg0

notes:
  The two push switches are simulating sensors. They could be ptb switches or wires over lapped - like antennae
