# Fritzing sketch id3803_simplified_h_bridge_0 (saved by Fritzing 0.9.3b)
breadboards: 1

parts:
  M1 = DC Motor  # not connected
  Q1 = TRANSISTOR_NPN [package=to-92-ammo]
  Q3 = TRANSISTOR_NPN [package=to-92]
  Q4 = TRANSISTOR_NPN [package=to-92]
  signals = Camdenboss CTB0158-2 [part_number="pin1 and 2" package=THT]
  Q2 = TRANSISTOR_NPN [package=sot223]

nets:
  N1: Q1.B, Q4.B, signals.pin1
  N2: Q1.C, Q2.C
  N3: Q3.E, Q4.E
  N4: Q3.B, signals.pin2, Q2.B
