# Fritzing sketch id3804_simulatore_gi_not_0 (saved by Fritzing 0.9.2b)
circuit board: 25.6532cm x 15.1511cm
breadboards: 3

parts:
  Q17 = pnp-Powertransistor [part_number=bdx94c package="TO220 [THT]"]
  R77 = Resistor [tolerance=±5% resistance=10k package=THT]
  R66 = Resistor [tolerance=±5% resistance=1M package=THT]
  R52 = Resistor [tolerance=±5% resistance=220 package=THT]
  R3 = Resistor [tolerance=±5% resistance=1M package=THT]
  R29 = Trimmer Potentiometer [maximum_resistance=6.8kΩ package=THT]
  R28 = Resistor [tolerance=±5% resistance=220 package=THT]
  Q11 = pnp-Powertransistor [part_number=bdx94c package="TO220 [THT]"]
  R79 = Resistor [tolerance=±5% resistance=10k package=THT]
  R27 = Resistor [tolerance=±5% resistance=470 package=THT]
  R42 = Resistor [tolerance=±5% resistance=860 package=THT]
  R73 = Resistor [tolerance=±5% resistance=220 package=THT]
  R71 = Trimmer Potentiometer [maximum_resistance=6.8kΩ package=THT]
  R43 = Resistor [tolerance=±5% resistance=470 package=THT]
  R68 = Resistor [tolerance=±5% resistance=220 package=THT]
  Q3 = NPN-Transistor [part_number="bc 337" package="TO92 [THT]"]
  U9 = Optocoupler [package=THT]
  R38 = Trimmer Potentiometer [maximum_resistance=10kΩ package=THT]
  R78 = Resistor [tolerance=±5% resistance=10k package=THT]
  R33 = Resistor [tolerance=±5% resistance=1M package=THT]
  LED8 = LED - 5mm [color="Red (633nm)" package="5 mm [THT]"]
  R55 = Resistor [tolerance=±5% resistance=330 package=THT]
  R37 = Trimmer Potentiometer [maximum_resistance=6.8kΩ package=THT]
  R40 = Resistor [tolerance=±5% resistance=1M package=THT]
  R5 = Resistor [tolerance=±5% resistance=220 package=THT]
  LED13 = LED - 5mm [color="Red (633nm)" package="5 mm [THT]"]
  Q4 = pnp-Powertransistor [part_number=bdx94c package="TO220 [THT]"]
  Q5 = pnp-Powertransistor [part_number=bdx94c package="TO220 [THT]"]
  LED21 = LED - 5mm [color="Red (633nm)" package="5 mm [THT]"]
  R41 = Resistor [tolerance=±5% resistance=220 package=THT]
  LED7 = LEDs [package=led10mm]
  R70 = Resistor [tolerance=±5% resistance=470 package=THT]
  U2 = Optocoupler [package=THT]
  R44 = Resistor [tolerance=±5% resistance=220 package=THT]
  R74 = Resistor [tolerance=±5% resistance=220 package=THT]
  Q10 = pnp-Powertransistor [part_number=bdx94c package="TO220 [THT]"]
  R39 = Resistor [tolerance=±5% resistance=330 package=THT]
  LED25 = LEDs [package=led10mm]
  R75 = Resistor [tolerance=±5% resistance=330 package=THT]
  LED20 = LED - 5mm [color="Red (633nm)" package="5 mm [THT]"]
  R36 = Resistor [tolerance=±5% resistance=220 package=THT]
  R30 = Trimmer Potentiometer [maximum_resistance=10kΩ package=THT]
  LED2 = LEDs [package=led10mm]
  R22 = Resistor [tolerance=±5% resistance=330 package=THT]
  Q7 = pnp-Powertransistor [part_number=bdx94c package="TO220 [THT]"]
  R7 = Resistor [tolerance=±5% resistance=220 package=THT]
  R46 = Trimmer Potentiometer [maximum_resistance=10kΩ package=THT]
  R4 = Resistor [tolerance=±5% resistance=860 package=THT]
  Q9 = NPN-Transistor [package="TO92 [THT]"]
  R53 = Trimmer Potentiometer [maximum_resistance=6.8kΩ package=THT]
  LED24 = LEDs [package=led10mm]
  Q14 = NPN-Transistor [package="TO92 [THT]"]
  U7 = Optocoupler [package=THT]
  Q6 = NPN-Transistor [package="TO92 [THT]"]
  Q8 = NPN-Transistor [package="TO92 [THT]"]
  LED16 = LEDs [package=led10mm]
  R47 = Resistor [tolerance=±5% resistance=330 package=THT]
  R13 = Trimmer Potentiometer [maximum_resistance=10kΩ package=THT]
  LED1 = LED - 5mm [color="Red (633nm)" package="5 mm [THT]"]
  R51 = Resistor [tolerance=±5% resistance=470 package=THT]
  R11 = Trimmer Potentiometer [maximum_resistance=6.8kΩ package=THT]
  LED12 = LEDs [package=led10mm]
  LED23 = LEDs [package=led10mm]
  R35 = Resistor [tolerance=±5% resistance=470 package=THT]
  R50 = Resistor [tolerance=±5% resistance=860 package=THT]
  U4 = Optocoupler [package=THT]
  R34 = Resistor [tolerance=±5% resistance=220 package=THT]
  U6 = Optocoupler [package=THT]
  R6 = Resistor [tolerance=±5% resistance=470 package=THT]
  LED14 = LED - 5mm [color="Red (633nm)" package="5 mm [THT]"]
  LED4 = LEDs [package=led10mm]
  R72 = Trimmer Potentiometer [maximum_resistance=6.8kΩ package=THT]
  R25 = Resistor [tolerance=±5% resistance=860 package=THT]
  R76 = Resistor [tolerance=±5% resistance=330 package=THT]
  R24 = Resistor [tolerance=±5% resistance=1M package=THT]
  R65 = Resistor [tolerance=±5% resistance=1M package=THT]
  U1 = Optocoupler [package=THT]
  R26 = Resistor [tolerance=±5% resistance=220 package=THT]
  Q15 = NPN-Transistor [package="TO92 [THT]"]
  U3 = Optocoupler [package=THT]
  R67 = Resistor [tolerance=±5% resistance=220 package=THT]
  LED11 = LEDs [package=led10mm]
  R81 = Resistor [tolerance=±5% resistance=860 package=THT]
  Q16 = pnp-Powertransistor [part_number=bdx94c package="TO220 [THT]"]
  Power_plug1 = Power plug
  R32 = Resistor [tolerance=±5% resistance=860 package=THT]
  Componente1 = Arduino Uno (Rev3)
  R31 = Resistor [tolerance=±5% resistance=330 package=THT]
  LED22 = LEDs [package=led10mm]
  R49 = Resistor [tolerance=±5% resistance=220 package=THT]
  SW2 = DIP Switch 8 Position [package=dipswitch-08]
  R48 = Resistor [tolerance=±5% resistance=1M package=THT]
  R80 = Resistor [tolerance=±5% resistance=10k package=THT]
  Q1 = NPN-Transistor [package="TO92 [THT]"]
  R69 = Resistor [tolerance=±5% resistance=470 package=THT]
  R45 = Trimmer Potentiometer [maximum_resistance=6.8kΩ package=THT]
  U8 = Voltage Regulator - 5V [package="TO220 [THT]"]
  LED15 = LEDs [package=led10mm]
  R54 = Trimmer Potentiometer [maximum_resistance=10kΩ package=THT]
  LED6 = LEDs [package=led10mm]
  LED5 = LED - 5mm [color="Red (633nm)" package="5 mm [THT]"]
  R64 = Resistor [tolerance=±5% resistance=860 package=THT]
  LED9 = LEDs [package=led10mm]
  LED10 = LEDs [package=led10mm]

nets:
  N1: Q17.base, Q15.C
  N2: Q17.collector, R76.Pin_1
  GND: R77.Pin_0, R29.leg2, R79.Pin_0, R42.Pin_1, R71.leg2, R78.Pin_0, LED8.cathode, LED21.cathode, LED7.C, LED25.C, LED20.cathode, R4.Pin_1, LED1.cathode, R11.leg2, R50.Pin_1, LED4.C, R72.leg2, R25.Pin_1, LED11.C, R81.Pin_1, Power_plug1.GND, R32.Pin_1, Componente1.GND, LED22.C, R80.Pin_0, U8.GND, LED15.C, LED5.cathode, R64.Pin_1, LED10.C
  N3: R77.Pin_1, Componente1.D2, SW2.16
  N4: R66.Pin_0, R68.Pin_0, R40.Pin_0, R65.Pin_0, R67.Pin_0, R49.Pin_0
  N5: R66.Pin_1, U6.Pin_6
  N6: R52.Pin_0, Q9.E
  N7: R52.Pin_1, R53.leg1, R53.wiper
  N8: R3.Pin_0, R33.Pin_0, R5.Pin_0, Q4.emitter, Q5.emitter, R41.Pin_0, R30.leg1, R30.wiper, R13.leg1, R13.wiper, R34.Pin_0, R24.Pin_0, R26.Pin_0, Power_plug1.VCC, U8.input_voltage
  N9: R3.Pin_1, U7.Pin_6
  N10: R29.leg1, R29.wiper, R28.Pin_1
  N11: R28.Pin_0, Q1.E
  N12: Q11.base, Q9.C, R54.leg2
  N13: Q11.collector, R55.Pin_1
  N14: Q11.emitter, R38.leg1, R38.wiper, Q10.emitter, Q7.emitter, R46.leg1, R46.wiper, Q16.emitter, R54.leg1, R54.wiper
  N15: R79.Pin_1, Componente1.D7, SW2.14
  N16: R27.Pin_0, U4.Pin_4, Q1.B
  N17: R27.Pin_1, LED5.anode
  N18: R42.Pin_0, U1.Pin_2
  N19: R73.Pin_0, Q14.E
  N20: R73.Pin_1, R71.leg1, R71.wiper
  N21: R43.Pin_0, Q8.B, U1.Pin_4
  N22: R43.Pin_1, LED13.anode
  N23: R68.Pin_1, U6.Pin_5
  N24: Q3.E, R7.Pin_0
  N25: Q3.B, U7.Pin_4, R6.Pin_0
  N26: Q3.C, Q4.base, R13.leg2
  N27: U9.Pin_1, Componente1.D13/SCK
  N28: U9.Pin_2, R81.Pin_0
  N29: U9.Pin_4, R70.Pin_0, Q15.B
  N30: U9.Pin_5, R67.Pin_1
  N31: U9.Pin_6, R65.Pin_1
  N32: R38.leg2, Q7.base, Q6.C
  N33: R78.Pin_1, Componente1.D4, SW2.15
  N34: R33.Pin_1, U2.Pin_6
  N35: LED8.anode, R35.Pin_1
  N36: R55.Pin_0, LED16.A
  N37: R37.leg1, LED13.cathode, R53.leg2, LED14.cathode, R45.leg2
  N38: R37.wiper, R37.leg2, R36.Pin_1
  N39: R40.Pin_1, U1.Pin_6
  N40: R5.Pin_1, U7.Pin_5
  N41: Q4.collector, R22.Pin_1
  N42: Q5.base, R30.leg2, Q1.C
  N43: Q5.collector, R31.Pin_1
  N44: LED21.anode, R70.Pin_1
  N45: R41.Pin_1, U1.Pin_5
  N46: LED7.A, LED6.C
  N47: U2.Pin_1, Componente1.D9_PWM
  N48: U2.Pin_2, R32.Pin_0
  N49: U2.Pin_4, Q6.B, R35.Pin_0
  N50: U2.Pin_5, R34.Pin_1
  N51: R44.Pin_0, Q8.E
  N52: R44.Pin_1, R45.leg1, R45.wiper
  N53: R74.Pin_0, Q15.E
  N54: R74.Pin_1, R72.leg1, R72.wiper
  N55: Q10.base, R46.leg2, Q8.C
  N56: Q10.collector, R47.Pin_1
  N57: R39.Pin_0, LED9.A
  N58: R39.Pin_1, Q7.collector
  N59: LED25.A, LED24.C
  N60: R75.Pin_0, LED23.A
  N61: R75.Pin_1, Q16.collector
  N62: LED20.anode, R69.Pin_1
  N63: R36.Pin_0, Q6.E
  N64: LED2.A, R22.Pin_0
  N65: LED2.C, LED4.A
  N66: R7.Pin_1, R11.leg1, R11.wiper
  N67: R4.Pin_0, U7.Pin_2
  N68: Q9.B, R51.Pin_0, U3.Pin_4
  N69: LED24.A, R76.Pin_0
  N70: Q14.B, U6.Pin_4, R69.Pin_0
  N71: Q14.C, Q16.base
  N72: U7.Pin_1, Componente1.D3_PWM
  N73: LED16.C, LED15.A
  N74: R47.Pin_0, LED12.A
  N75: LED1.anode, R6.Pin_1
  N76: R51.Pin_1, LED14.anode
  N77: LED12.C, LED11.A
  N78: LED23.C, LED22.A
  N79: R50.Pin_0, U3.Pin_2
  N80: U4.Pin_1, Componente1.D5_PWM
  N81: U4.Pin_2, R25.Pin_0
  N82: U4.Pin_5, R26.Pin_1
  N83: U4.Pin_6, R24.Pin_1
  N84: U6.Pin_1, Componente1.D12/MISO
  N85: U6.Pin_2, R64.Pin_0
  N86: U1.Pin_1, Componente1.D10_PWM/SS
  N87: U3.Pin_1, Componente1.D11_PWM/MOSI
  N88: U3.Pin_5, R49.Pin_1
  N89: U3.Pin_6, R48.Pin_1
  N90: Componente1.D6_PWM, SW2.13, R80.Pin_1
  N91: Componente1.5V, SW2.1, SW2.2, SW2.3, SW2.4, U8.output_voltage
  N92: R31.Pin_0, LED6.A
  N93: LED9.C, LED10.A

notes:
  Vcc 12V ----
  simulatore di
  alba-giorno-tramonto-notte
  perpresepi o plastici di tutti i tipi
  i led24 e 25 possono essere di qualsiasi coloree dimensione.
  attenzione a r76 deve essere dimensionata per la tensione e per il numero di diodi led utilizzati.
  questo vale per tutti i canali
  canale "attività umane" (on-off)
  canale "fuoco" (on-off)
  canale"notte"
  fade
  canale "tramonto"
  fade
  canale "giorno" fade
  canale "giorno esteso"
  ( Alba+giorno+tramonto)
  fade
  canale "alba"
  fade
  Con questa configurazione di transistor si possono avere fino a 50w per canale. Ma si deve prevedere una corretta dissipazione dei finali.
  R11 regolazione della corrente massima
  R29 regolazione del punto di accensione (luminosità)
