# Fritzing sketch id3805_knightrider_0 (saved by Fritzing 0.7.12b)
breadboards: 1

parts:
  IC1 = IC, DIP package, 8 pins [chip_label=tiny13A spacing=300mil]
  LED1 = LED - 5mm [color="Red (633nm)" package="5 mm [THT]"]
  LED2 = LED - 5mm [color="Red (633nm)" package="5 mm [THT]"]
  LED3 = LED - 5mm [color="Red (633nm)" package="5 mm [THT]"]
  LED4 = LED - 5mm [color="Red (633nm)" package="5 mm [THT]"]
  LED5 = LED - 5mm [color="Red (633nm)" package="5 mm [THT]"]
  R1 = Resistor [tolerance=±5% resistance=150 package=THT]
  J1 = male pin header, 6 pins [form="♂ (male)"]
  C1 = Ceramic Capacitor [capacitance=100nF package="100 mil [THT, multilayer]"]
  J2 = male pin header, 6 pins [form="♂ (male)"]
  J4 = shrouded pin header, 6 pins [form="♂ (shrouded male)"]

nets:
  N1: IC1.pin1, J1.pin2
  N2: IC1.pin2, LED4.cathode
  N3: IC1.pin3, LED5.cathode
  N4: IC1.pin4, J1.pin1, C1.1
  N5: IC1.pin5, LED3.cathode, J1.pin6
  N6: IC1.pin6, LED2.cathode, J1.pin5
  N7: IC1.pin7, LED1.cathode, J1.pin4
  N8: IC1.pin8, R1.Pin_1, J1.pin3, C1.0
  N9: LED1.anode, LED2.anode, LED3.anode, LED4.anode, LED5.anode, R1.Pin_0
  N10: J2.pin1, J4.pin4
  N11: J2.pin2, J4.pin3
  N12: J2.pin3, J4.pin6
  N13: J2.pin4, J4.pin2
  N14: J2.pin5, J4.pin1
  N15: J2.pin6, J4.pin5

notes:
  Breadboard ISP for ATtiny13A
  ISP conversion cable
