# Fritzing sketch id3806_rpi_led_0 (saved by Fritzing 0.7.12b)
breadboards: 1

parts:
  Pi1 = Pi_Cobbler
  R1 = Resistor [tolerance=±5% resistance=680 package=THT]
  LED1 = LED - 5mm [color="Red (633nm)" package="5 mm [THT]"]

nets:
  N1: Pi1.connector1, R1.Pin_0
  N2: Pi1.connector6, LED1.cathode
  N3: R1.Pin_1, LED1.anode
