# Fritzing sketch id3807_DualTrackingPS_0 (saved by Fritzing 0.9.3b)
perfboards: 1

parts:
  U1 = Voltage Regulator [part_number=LM317 package=to220-adj]
  D1 = Rectifier Diode [part_number=1N4001 package="300 mil [THT]"]
  R1 = Resistor [tolerance=±5% resistance=220 package=THT]
  C1 = Electrolytic Capacitor [capacitance=10µF voltage=50V package="100 mil [THT, electrolytic]"]
  U2 = LM 358 Dual Op-Amp [part_number=LM358 package="DIP8 [THT]"]
  R3 = Resistor [tolerance=±5% resistance=10k package=THT]
  R4 = Resistor [tolerance=±5% resistance=10k package=THT]
  R5 = Resistor [tolerance=±5% resistance=10k package=THT]
  R6 = Resistor [tolerance=±5% resistance=100k package=THT]
  R7 = Resistor [tolerance=±5% resistance=100k package=THT]
  R8 = Resistor [tolerance=±5% resistance=10k package=THT]
  R9 = Resistor [tolerance=±5% resistance=10k package=THT]
  R10 = Resistor [tolerance=±5% resistance=0.1 power=1W package=THT]
  R2 = Rotary Potentiometer (Small) [maximum_resistance=5kΩ part_number="Output Adj" package=THT]
  D2 = Rectifier Diode [part_number=1N4184 package="300 mil [THT]"]
  D3 = Rectifier Diode [part_number=1N4184 package="300 mil [THT]"]
  Q2 = PNP-Transistor [part_number=A965 package="TO92 [THT]"]
  R11 = Resistor [tolerance=±5% resistance=100 power=1W package=THT]
  D4 = Rectifier Diode [part_number=1N4001 package="300 mil [THT]"]
  V1 = DC Power [voltage=70V]
  C2 = Electrolytic Capacitor [voltage=50V part_number=3300uF package="300 mil [THT, electrolytic]"]
  C3 = Electrolytic Capacitor [voltage=50V part_number=3300uF package="300 mil [THT, electrolytic]"]
  R12 = Resistor [tolerance=±5% resistance=4.7k power=1W package=THT]
  Q1 = pnp-Powertransistor [part_number=B1273 package="TO220 [THT]"]
  C4 = Electrolytic Capacitor [capacitance=10µF voltage=50V package="100 mil [THT, electrolytic]"]
  J2 = female pin header, 2 pins [form="♀ (female)" part_number="1.2 to 15V"]
  J1 = female pin header, 2 pins [form="♀ (female)"]
  J1_2 = female pin header, 2 pins [form="♀ (female)" part_number="-1.2 to -15V"]

nets:
  N1: U1.ADJ, R1.Pin_0, R2.leg1, R2.wiper
  N2: U1.IN, D1.cathode, U2.connector7, V1.V+, C3.+
  N3: U1.OUT, D1.anode, R1.Pin_1, C1.+, R3.Pin_0, J2.pin2
  GND: C1.-, U2.connector2, R6.Pin_1, R2.leg2, C2.+, C3.-, C4.+, J2.pin1, J1.pin2, J1_2.pin2
  N4: U2.connector0, D3.anode
  N5: U2.connector1, R3.Pin_1, R4.Pin_0
  N6: U2.connector3, V1.V-, C2.-, R12.Pin_0
  N7: U2.connector4, R6.Pin_0, R8.Pin_1
  N8: U2.connector5, R7.Pin_0, R9.Pin_1
  N9: U2.connector6, R7.Pin_1, D2.anode
  N10: R4.Pin_1, R5.Pin_0
  N11: R5.Pin_1, R8.Pin_0, R10.Pin_0, C4.-, J1.pin1, J1_2.pin1
  N12: R9.Pin_0, R10.Pin_1, D4.cathode, Q1.emitter
  N13: D2.cathode, D3.cathode
  N14: Q2.E, Q1.base
  N15: Q2.B, R12.Pin_1
  N16: Q2.C, R11.Pin_0
  N17: R11.Pin_1, D4.anode, Q1.collector
