# Fritzing sketch id3808_arduino_single_servo_control_0 (saved by Fritzing 0.9.2b)
breadboards: 1

parts:
  Part1 = Arduino Uno (Rev3) - ICSP
  J1 = Basic Servo

nets:
  N1: Part1.D9_PWM, J1.pulse
  5V: Part1.5V, J1.vcc
  GND: Part1.GND, J1.gnd
