# Fritzing sketch id3809_LittleWire_0 (saved by Fritzing 0.7.4b)
breadboards: 1

parts:
  U1 = attiny85 [package=dip]
  R1 = Resistor [tolerance=±5% resistance=33 package=THT]
  R3 = Resistor [tolerance=±5% resistance=1.5k package=THT]
  R2 = Resistor [tolerance=±5% resistance=33 package=THT]
  D1 = Zener Diode [part_number=1N4732A breakdown_voltage=3.6V package="300 mil [THT]"]
  D2 = Zener Diode [part_number=1N4732A breakdown_voltage=3.6V package="300 mil [THT]"]
  J1 = male pin header, 2 pins [form="♂ (male)"]
  C2 = Electrolytic Capacitor [capacitance=100nF voltage=10V package="100 mil [THT, electrolytic]"]
  C1 = Electrolytic Capacitor [capacitance=100nF voltage=10V package="100 mil [THT, electrolytic]"]
  CONN1 = USB_connector
  LED1 = LED - 5mm [color="Red (633nm)" package="5 mm [THT]"]
  R4 = Resistor [tolerance=±5% resistance=220 package=THT]
  J2 = Generic_shrouded_header___6_pins [form="♂ (shrouded male)"]

nets:
  N1: U1.Pin_1, J2.connector4
  N2: U1.Pin_2, R1.Pin_0, R3.Pin_1, D2.cathode
  N3: U1.Pin_3, R2.Pin_0, D1.cathode
  GND: U1.Pin_4, D1.anode, D2.anode, C2.-, C1.-, CONN1.connector3, R4.Pin_1, J2.connector5
  N4: U1.Pin_5, J2.connector3
  N5: U1.Pin_6, J2.connector0
  N6: U1.Pin_7, J2.connector2
  5V: U1.Pin_8, R3.Pin_0, J1.pin2, C2.+, C1.+, CONN1.connector0, LED1.anode
  N7: R1.Pin_1, CONN1.connector1
  N8: R2.Pin_1, CONN1.connector2
  N9: J1.pin1, J2.connector1
  N10: LED1.cathode, R4.Pin_0
