# Fritzing sketch id380_3V_Motor_Control_Advanced_0 (saved by Fritzing 0.9.2b)
breadboards: 1

parts:
  Part1 = Arduino Uno (Rev3)  # not connected
  D1 = Rectifier Diode [part_number=1N4001 package="300 mil [THT]"]
  Q1 = NPN-Transistor [package="SOT-23 [SMD]"]
  R1 = Resistor [tolerance=±5% resistance=220 package=THT]
  M1 = DC Motor
  R2 = Resistor [tolerance=±5% resistance=10k package=THT]

nets:
  N1: D1.cathode, M1.pin_1
  N2: D1.anode, Q1.1, M1.pin_2
  N3: Q1.2, R2.Pin_0
  N4: Q1.0, R1.Pin_1
