# Fritzing sketch id3810_SeguiLSol_0 (saved by Fritzing 0.8.7b)
breadboards: 1

parts:
  Part1 = Arduino Mega 2560 (Rev3)
  C2 = Capacitor Polarized [package=panasonic_g]
  M1 = Stepper Motor - Bipolar
  MD09B1 = A4988 Stepper Motor Driver Carrier
  J2 = Screw terminal - 2 pins [package=THT]

nets (from the breadboard view):
  N1: Part1.GND, C2.-, MD09B1.GROUND, J2.pin1
  VIN: Part1.VIN, MD09B1.MS1, MD09B1.MS2, MD09B1.MS3, MD09B1.VDD
  N2: Part1.D2_PWM, MD09B1.DIR
  N3: Part1.D3_PWM, MD09B1.STEP
  N4: Part1.D6_PWM, MD09B1.Enable
  N5: C2.+, MD09B1.VMOT, J2.pin2
  N6: M1.A, MD09B1.OUT_2A
  N7: M1.C, MD09B1.OUT_2B
  N8: M1.B, MD09B1.OUT_1A
  N9: M1.D, MD09B1.OUT_1B
  N10: MD09B1.RESET, MD09B1.SLEEP

notes:
  motor power supply
  8-35V
