# Fritzing sketch id3811_Single_Transistor___15_Db_Audio_Amp_0 (saved by Fritzing 0.6.3b)
breadboards: 1

parts:
  Q1 = NPN-Transistor [part_number=BC548B package="TO92 [THT]"]
  C1 = Ceramic Capacitor [capacitance=1µF package="100 mil [THT, multilayer]"]
  J1-_Input = female pin header, 2 pins [form="♀ (female)"]
  R1 = Resistor [tolerance=±5% resistance=330k package=THT]
  R2 = Resistor [tolerance=±5% resistance=100k package=THT]
  R4 = Resistor [tolerance=±5% resistance=330 package=THT]
  R5 = Resistor [tolerance=±5% resistance=150 package=THT]
  C2 = Electrolytic Capacitor [capacitance=0.22mF voltage=20V package="100 mil [THT, electrolytic]"]
  R3 = Resistor [tolerance=±5% resistance=2.2k package=THT]
  C2_2 = Ceramic Capacitor [capacitance=10µF package="100 mil [THT, multilayer]"]
  J2_-Output = female pin header, 2 pins [form="♀ (female)"]
  J3_-_Power = female pin header, 2 pins [form="♀ (female)"]
  S1 = Toggle Switch [package=THT]
  R6 = Resistor [tolerance=±5% resistance=680 package=THT]
  LED1 = LED - 5mm [color="Red (633nm)" package="5 mm [THT]"]

nets:
  N1: Q1.E, R3.Pin_1, C2_2.0
  N2: Q1.B, C1.1, R1.Pin_1, R2.Pin_0
  N3: Q1.C, R4.Pin_0
  N4: C1.0, J1-_Input.pin2
  N5: J1-_Input.pin1, R2.Pin_1, R5.Pin_1, C2.-, J2_-Output.pin2, J3_-_Power.pin1, LED1.cathode
  N6: R1.Pin_0, R3.Pin_0
  N7: R4.Pin_1, R5.Pin_0, C2.+
  N8: C2_2.1, J2_-Output.pin1
  N9: J3_-_Power.pin2, S1.L2
  N10: S1.COM, R6.Pin_0
  N11: R6.Pin_1, LED1.anode

notes:
  Power Supply is 9Vdc
