# Fritzing sketch id3812_einfsevensegteljari_0 (saved by Fritzing 0.8.5b)
breadboards: 1

parts:
  Part1 = Arduino Uno (Rev3)
  S1 = Pushbutton [package="[THT]"]
  R1 = Resistor [tolerance=±5% resistance=220 package=THT]
  7_Segment1 = 7 Segment Display
  R2 = Resistor [tolerance=±5% resistance=100 package=THT]

nets:
  N1: Part1.D8, 7_Segment1.Segment_G
  N2: Part1.D9_PWM, 7_Segment1.Segment_DP
  N3: Part1.D12/MISO, S1.Pin_1, S1.Pin_2, R1.Pin_0
  N4: Part1.GND, R1.Pin_1, R2.Pin_1
  N5: Part1.D2, 7_Segment1.Segment_B
  N6: Part1.D3_PWM, 7_Segment1.Segment_A
  N7: Part1.D4, 7_Segment1.Segment_C
  N8: Part1.D5_PWM, 7_Segment1.Segment_D
  N9: Part1.D6_PWM, 7_Segment1.Segment_E
  N10: Part1.D7, 7_Segment1.Segment_F
  N11: Part1.5V, S1.Pin_3, S1.Pin_4
  N12: 7_Segment1.common_anode, R2.Pin_0
