# Fritzing sketch id3813_siz_0 (saved by Fritzing 0.9.3b)
breadboards: 1

parts:
  U2 = PCF8574 [package="DIP16 [THT]"]
  U3 = PCF8574 [package="DIP16 [THT]"]
  LCD1 = LCD screen
  Часть1 = Arduino Nano (Rev3.0) (ICSP)
  R1 = Trimmer Potentiometer [maximum_resistance=10kΩ package=THT]
  S1 = Pushbutton [package=THT]
  S2 = Pushbutton [package=THT]
  S3 = Pushbutton [package=THT]
  S4 = Pushbutton [package=THT]
  S5 = Pushbutton [package=THT]
  S6 = Pushbutton [package=THT]
  S7 = Pushbutton [package=THT]
  S8 = Pushbutton [package=THT]
  S9 = Pushbutton [package=THT]
  S10 = Pushbutton [package=THT]
  S11 = Pushbutton [package=THT]
  S12 = Pushbutton [package=THT]
  S13 = Pushbutton [package=THT]
  S14 = Pushbutton [package=THT]
  S15 = Pushbutton [package=THT]
  S16 = Pushbutton [package=THT]
  R2 = Resistor [tolerance=±5% resistance=220 package=THT]
  C1 = Ceramic Capacitor [capacitance=100nF package="100 mil [THT, multilayer]"]
  C2 = Ceramic Capacitor [capacitance=100nF package="100 mil [THT, multilayer]"]
  R3 = Resistor [tolerance=±0.25% resistance=50 package=THT]
  U4 = Transformer [package=transformer_smd]
  U5 = Transformer [package=transformer]
  J$1 = SMA Antenna Connector [package=sma-edge]
  J$2 = SMA Antenna Connector [package=sma-edge]
  ANT1 = Antenna
  U6 = Hirose DF13 Series Header [part_number="s meter" package=DF13C-2P-1.25V]
  U7 = Hirose DF13 Series Header [part_number=VCC package=DF13C-2P-1.25V]
  U8 = TRANSISTOR_NPN [package=sot23]
  C3 = Ceramic Capacitor [capacitance=100nF package="100 mil [THT, multilayer]"]
  C4 = Ceramic Capacitor [capacitance=100nF package="100 mil [THT, multilayer]"]
  R4 = Resistor [tolerance=±5% resistance=33k package=THT]
  R5 = Resistor [tolerance=±5% resistance=3.3k package=THT]
  D1 = Rectifier Diode [part_number=1N4001 package="300 mil [THT]"]
  D2 = Rectifier Diode [part_number=1N4001 package="300 mil [THT]"]
  R6 = Resistor [tolerance=±5% resistance=1k package=THT]
  R7 = Resistor [tolerance=±5% resistance=1k package=THT]
  R8 = Resistor [tolerance=±5% resistance=1k package=THT]
  U9 = OPA344 [package=sot23-5]
  U10 = OPA344 [package=sot23-5]
  R9 = Resistor [tolerance=±5% resistance=1k package=THT]
  R10 = Resistor [tolerance=±5% resistance=1k package=THT]
  R11 = Resistor [tolerance=±5% resistance=1k package=THT]
  D4 = Rectifier Diode [part_number=1N4001 package="300 mil [THT]"]
  D5 = Rectifier Diode [part_number=1N4001 package="300 mil [THT]"]
  D6 = Rectifier Diode [part_number=1N4001 package="300 mil [THT]"]
  D7 = Rectifier Diode [part_number=1N4001 package="300 mil [THT]"]
  M1 = Stepper Motor - Bipolar
  К_плате_диапазонных_фильтров_595x2 = 74HC595 [package="DIP16 [THT]"]
  U12 = Voltage Regulator - 5V [package="TO220 [THT]"]
  Power_plug1 = Power plug
  Синтезатор_укв = LM7001 [part_number=LM7001]
  U14 = Hirose DF13 Series Header [part_number="1 ПЧ" package=DF13C-2P-1.25V]
  U15 = Hirose DF13 Series Header [part_number="2 ПЧ" package=DF13C-2P-1.25V]
  U16 = Hirose DF13 Series Header [part_number=ГУН package=DF13C-2P-1.25V]
  U17 = Molex Picoblade Series Header [part_number="PWR УМ" package=Picoblade-53398-0271]
  U18 = Molex Picoblade Series Header [part_number=PWM package=Picoblade-53398-0271]
  C5 = Electrolytic Capacitor [capacitance=100µF voltage=35V package="0405 [SMD, electrolytic]"]
  C6 = Ceramic Capacitor [capacitance=100nF package="100 mil [THT, multilayer]"]
  part = Molex Picoblade Series Header [part_number="TO VCC" package=Picoblade-53398-0271]
  C7 = Electrolytic Capacitor [capacitance=999µF voltage=35V package="100 mil [THT, electrolytic]"]
  part_2 = adafruit [part_number="Синтезатор КВ +  ПЧ"]
  Q1 = MOSFET-NCHANNEL [package=to220v]
  Q2 = MOSFET-NCHANNEL [package=to220v]
  1117 = V_REG_LD1117VXX [package=78xxl]
  7805 = Voltage Regulator [package=to-92]
  C8 = Electrolytic Capacitor [capacitance=100µF voltage=50V package="100 mil [THT, electrolytic]"]
  C9 = Electrolytic Capacitor [capacitance=100µF voltage=50V package="100 mil [THT, electrolytic]"]
  C10 = Electrolytic Capacitor [capacitance=100µF voltage=50V package="100 mil [THT, electrolytic]"]
  C11 = Ceramic Capacitor [capacitance=100nF package="100 mil [THT, multilayer]"]
  C12 = Ceramic Capacitor [capacitance=100nF package="100 mil [THT, multilayer]"]
  R12 = Resistor [tolerance=±5% resistance=1k package=THT]
  R13 = Resistor [tolerance=±5% resistance=1k package=THT]
  C13 = Ceramic Capacitor [capacitance=100nF voltage=50V package="200 mil [THT, multilayer]"]
  part_3 = Molex Picoblade Series Header [part_number=Основное package=Picoblade-53261-0219]
  part_4 = Molex Picoblade Series Header [part_number="Опорное 1 пч" package=Picoblade-53261-0219]
  part_5 = Molex Picoblade Series Header [part_number="Опорное 2 пч" package=Picoblade-53261-0219]

nets:
  GND: U2.A0, U2.A1, U2.A3, U2.GND, U3.GND, LCD1.VSS, R1.leg1, C1.0, C2.0, R3.Pin_0, J$1.GND, J$2.GND, U6.2, U7.2, U8.E, C3.0, C4.0, R5.Pin_0, R8.Pin_0, U10.V-, К_плате_диапазонных_фильтров_595x2.GND, Синтезатор_укв.connector15, U14.2, U15.2, U16.2, U17.2, U18.2, part_2.connector55, 1117.GND, 7805.GND, C8.-, C9.-, C10.-, C11.0, C12.0, C13.0, part_3.2, part_4.2, part_5.2
  N1: U2.P0, LCD1.RS
  N2: U2.P1, LCD1.R/W
  N3: U2.P2, LCD1.E
  N4: U2.P3, U8.B
  N5: U2.P4, LCD1.DB4
  N6: U2.P5, LCD1.DB5
  N7: U2.P6, LCD1.DB6
  N8: U2.P7, LCD1.DB7
  N9: U2.SCL, U3.SCL, Часть1.A5, Q2.D
  N10: U2.SDA, U3.SDA, Часть1.A4, Q1.D
  5V: U2.VCC, U3.A0, U3.A1, U3.A3, LCD1.VDD, LCD1.LED+, R1.leg2, U9.V-, R11.Pin_1, К_плате_диапазонных_фильтров_595x2.VCC, Синтезатор_укв.connector11, Синтезатор_укв.connector12
  N11: U3.P0, S1.leg1, S5.leg1, S9.leg1, S13.leg1
  N12: U3.P1, S2.leg1, S6.leg1, S10.leg1, S14.leg1
  N13: U3.P2, S3.leg1, S7.leg1, S11.leg1, S15.leg1
  N14: U3.P3, S4.leg1, S8.leg1, S12.leg1, S16.leg1
  N15: U3.P4, S1.leg0, S2.leg0, S3.leg0, S4.leg0
  N16: U3.P5, S5.leg0, S6.leg0, S7.leg0, S8.leg0
  N17: U3.P6, S9.leg0, S10.leg0, S11.leg0, S12.leg0
  N18: U3.P7, S13.leg0, S14.leg0, S15.leg0, S16.leg0
  N19: LCD1.V0, R1.wiper
  N20: LCD1.LED-, U8.C
  N21: Часть1.D2, R7.Pin_1
  N22: Часть1.D3, R6.Pin_1
  N23: Часть1.D4, К_плате_диапазонных_фильтров_595x2.SH_CP
  N24: Часть1.D5, К_плате_диапазонных_фильтров_595x2.ST_CP
  N25: Часть1.D6, К_плате_диапазонных_фильтров_595x2.DS
  N26: Часть1.D7, Синтезатор_укв.connector4
  N27: Часть1.D8, Синтезатор_укв.connector3
  N28: Часть1.D9, Синтезатор_укв.connector2
  N29: Часть1.D10, U17.1
  N30: Часть1.D11/MOSI, U18.1
  N31: Часть1.VIN, U12.output_voltage, C5.+, C6.1
  N32: Часть1.A7, C2.1, D1.cathode
  N33: Часть1.A6, C1.1, D2.cathode
  N34: Часть1.A3, R2.Pin_0
  N35: Часть1.A2, R4.Pin_0, R5.Pin_1
  N36: R2.Pin_1, U6.1, C3.1
  N37: R3.Pin_1, U4.2, U5.1
  N38: U4.1, D2.anode
  N39: U4.3, U5.4
  N40: U4.4, J$1.SIGNAL, ANT1.antenna_lead
  N41: U5.2, D1.anode
  N42: U5.3, J$2.SIGNAL
  N43: U7.1, C4.1, R4.Pin_1
  N44: R6.Pin_0, U9.OUT
  N45: R7.Pin_0, U10.OUT
  N46: R8.Pin_1, U9.-IN, U10.-IN, R11.Pin_0, D4.anode, D5.cathode, D6.cathode, D7.anode, M1.C, M1.B
  N47: U9.+IN, R9.Pin_1
  N48: U10.+IN, R10.Pin_1
  N49: R9.Pin_0, D6.anode, D7.cathode, M1.A
  N50: R10.Pin_0, D4.cathode, D5.anode, M1.D
  N51: U12.input_voltage, Power_plug1.VCC, part.1, C7.+, 7805.IN, C9.+, C13.1
  GND_2: U12.GND, Power_plug1.GND, C5.-, C6.0, part.2, C7.-
  N52: Синтезатор_укв.connector10, U16.1
  N53: Синтезатор_укв.connector13, U15.1
  N54: Синтезатор_укв.connector14, U14.1
  N55: part_2.connector10, Q1.G, Q2.G, 1117.OUT, C10.+, C11.1, R12.Pin_1, R13.Pin_1
  N56: part_2.connector12, Q1.S, R13.Pin_0
  N57: part_2.connector13, Q2.S, R12.Pin_0
  N58: part_2.connector16, part_3.1
  N59: part_2.connector53, part_4.1
  N60: part_2.connector56, part_5.1
  N61: 1117.IN, 7805.OUT, C8.+, C12.1

notes:
  к УМ
