# Fritzing sketch id3817_Sistema_de_adquisicion_de_datos_FPGA_0 (saved by Fritzing 0.9.3b)
perfboards: 1

parts:
  U5 = Voltage Regulator - 5V [package="DPak [SMD]"]  # not connected
  U6 = Voltage Regulator - 5V [package="DPak [SMD]"]
  JP1 = Header 10 [package=1x10-2mm-smd]
  JP2 = Header 10 [package=1x10-2mm-smd]  # not connected
  JP3 = Header 10 [package=1x10-2mm-smd]  # not connected
  JP4 = Header 10 [package=1x10-2mm-smd]  # not connected

nets:
  N1: U6.input_voltage, JP1.3
  N2: U6.output_voltage, JP1.2

notes:
  LTC1290
  LM7805
  LM7905
  FPGA Inputs
