# Fritzing sketch id3818_sistema_disparo_0 (saved by Fritzing 0.9.3b)
breadboards: 1

parts:
  Componente1 = Arduino Uno (Rev3)
  Componente2 = Logic Level Converter
  R1 = Resistor [tolerance=±5% resistance=100 package=THT]
  R2 = Resistor [tolerance=±5% resistance=1k package="2010 [SMD]"]
  KY-1 = keyes
  TRRS1 = Audio Jack (TRRS) 3.5mm [part_number="LUMBERG JEITA RC-5325A" package="RC-5325A [SMD]"]
  TRRS2 = Audio Jack (TRRS) 3.5mm [part_number="LUMBERG JEITA RC-5325A" package="RC-5325A [SMD]"]
  JP1 = Header 10 [package=1x10-2mm-smd]

nets:
  GND: Componente1.GND, Componente2.GND, R2.Pin_1, KY-1.connector2, JP1.5
  N1: Componente1.D2, R2.Pin_0, JP1.2
  N2: Componente1.D4, KY-1.connector0
  N3: Componente1.D7, Componente2.TX_HV
  N4: Componente1.3V3, Componente2.LV
  N5: Componente1.5V, KY-1.connector1
  N6: Componente2.TX_LV, R1.Pin_1
  N7: R1.Pin_0, JP1.9
  N8: KY-1.connector3, TRRS1.RING2, TRRS2.RING2
  N9: KY-1.connector4, TRRS1.RING1, TRRS2.RING1

notes:
  Comunicação SPAN:
  IN (ciano)
  GND (preto)
  OUT (laranja)
  Saídas para as câmeras esquerda/direita
