# Fritzing sketch id3819_Proyecto_De_Riego_Inteligente_0 (saved by Fritzing 0.9.3b)
breadboards: 1

parts:
  Componente1 = Arduino Mega 2560 (Rev3)
  Q1 = NPN-Transistor [package="TO92 [THT]"]
  R1 = Resistor [tolerance=±5% resistance=1k package=THT]
  U5 = RELAY [package=relay-jzc]
  Power_plug1 = Power plug
  M1 = DC Motor
  IC2 = IC, DIP package, 8 pins [chip_label=IC]  # not connected

nets:
  N1: Componente1.D9_PWM, R1.Pin_1
  N2: Componente1.5V, Q1.C
  N3: Componente1.GND, U5.COIL2
  N4: Q1.E, U5.COIL1
  N5: Q1.B, R1.Pin_0
  N6: U5.NO, M1.pin_2
  N7: U5.MAIN, Power_plug1.VCC
  N8: Power_plug1.GND, M1.pin_1

notes:
  Bomba de agua
  12 VDC
  POWER SUPPLY
  12 VDC
