# Fritzing sketch id3821_Seis_servos_com_pot_0 (saved by Fritzing 0.7.7b)
breadboards: 1

parts:
  Arduino1 = Arduino
  R1 = Rotary Potentiometer (Small) [maximum_resistance=10kΩ]
  R2 = Rotary Potentiometer (Small) [maximum_resistance=10kΩ]
  R3 = Rotary Potentiometer (Small) [maximum_resistance=10kΩ]
  VCC1 = 4 x AAA Battery Mount
  J1 = Basic Servo
  J2 = Basic Servo
  J3 = Basic Servo
  J4 = Basic Servo
  J5 = Basic Servo
  J6 = Basic Servo
  R4 = Rotary Potentiometer (Small) [maximum_resistance=10kΩ]
  R5 = Rotary Potentiometer (Small) [maximum_resistance=10kΩ]
  R6 = Rotary Potentiometer (Small) [maximum_resistance=10kΩ]

nets:
  GND: Arduino1.GND, R1.leg2, R2.leg2, R3.leg2, VCC1.-, J1.gnd, J2.gnd, J3.gnd, J4.gnd, J5.gnd, J6.gnd, R4.leg2, R5.leg2, R6.leg2
  N1: Arduino1.D11, J6.pulse
  N2: Arduino1.D10, J4.pulse
  N3: Arduino1.D9, J2.pulse
  N4: Arduino1.D5, J5.pulse
  N5: Arduino1.D4, J3.pulse
  N6: Arduino1.+5V, R1.leg1, R2.leg1, R3.leg1, R4.leg1, R5.leg1, R6.leg1
  N7: Arduino1.A0, R1.wiper
  N8: Arduino1.A1, R2.wiper
  N9: Arduino1.A2, R3.wiper
  N10: Arduino1.A3, R4.wiper
  N11: Arduino1.A4, R5.wiper
  N12: Arduino1.A5, R6.wiper
  VCC: VCC1.+, J1.vcc, J2.vcc, J3.vcc, J4.vcc, J5.vcc, J6.vcc
