# Fritzing sketch id3824_Skype_Busy_Lamp_0 (saved by Fritzing 0.9.3b)
circuit board: 6.88566cm x 5.36311cm
breadboards: 1

parts:
  BLU = Basic FET N-Channel [package="TO220 [THT]"]
  GRN = Basic FET N-Channel [package="TO220 [THT]"]
  RED = Basic FET N-Channel [package="TO220 [THT]"]
  JP1 = Header 4 [package=molex-1x4_lock]
  Part1 = Arduino Uno (Rev3)

nets:
  N1: BLU.gate, Part1.D3_PWM
  N2: BLU.drain, GRN.drain, RED.drain, JP1.1, JP1.2, JP1.3, JP1.4, Part1.VIN
  N3: BLU.source, GRN.source, RED.source, Part1.D13/SCK, Part1.GND
  N4: GRN.gate, Part1.D5_PWM
  N5: RED.gate, Part1.D6_PWM

notes:
  ramblinggeek.co.uk
  Feb. 2018, rev 1
  PWR
