# Fritzing sketch id3826_sleepez_0 (saved by Fritzing 0.9.2b)
circuit board: 8.46667cm x 5.64444cm
breadboards: 1

parts:
  Edison = Intel Edison Arduinobreakout
  Sound_Sensor = Breakout Board for Electret Microphone
  VCC1 = Battery
  SP1 = SPEAKER [package=pcb_mount_speaker]

nets:
  N1: Edison.A0, Sound_Sensor.AUD
  GND: Edison.GND, Sound_Sensor.GND, VCC1.-, SP1.-
  N2: Edison.D1/TX, SP1.+
  5V: Edison.5V, Sound_Sensor.VCC
  N3: Edison.VIN, VCC1.+
