# Fritzing sketch id3827_Fairy_0 (saved by Fritzing 0.8.7b)
breadboards: 1

parts:
  J1 = Piezo Speaker
  C1 = Capacitor [package=cap-pth-small2]
  Part1 = LilyPad Coin Cell Battery Holder
  FLICKER_LED = LED - 5mm [color="Red (633nm)" package="5 mm [THT]"]
  D1 = Schottky Diode [part_number=1N5817 package="Melf DO-213 AB [SMD]"]
  Q1 = Matt's-NChannel

nets:
  N1: J1.pin1, C1.1, Part1.-, Q1.connector1
  N2: J1.pin2, D1.anode
  N3: C1.2, D1.cathode, Q1.connector2
  N4: Part1.+, FLICKER_LED.anode
  N5: FLICKER_LED.cathode, Q1.connector0

notes:
  Warming or cooling the piezo causes a small volate onto the mosfet. The excess is stored in the cap.
  This circuit takes advantage of the enhanced mosfets "leakage" as a random timer. that keeps the fairy awake for a short time.
  These are the "fairy's toes". Stroking these with your finger removes the charge at the mosfet gate, and puts the fairy back to sleep. Shorting these, is nearly equivalent to turning the fairy off.
  The LED I use is the candle flicker leds, that pulse like a candle by a small micro in the head.
