# Fritzing sketch id3828_Untitled_Sketch_0 (saved by Fritzing 0.9.3b)
circuit board: 12.1627cm x 6.86925cm
breadboards: 1

parts:
  NANO = Arduino Nano (Rev3.0)
  DREHENCODER = Rotary_Encoder_with_Knob
  POTI = Rotary Encoder [package=THT]
  DISPLAY = female pin header, 4 pins [form="♀ (female)"]
  Vin = female pin header, 2 pins [form="♀ (female)"]
  Stepper = Pololu A4988 [package=SO16]
  SteppOut = female pin header, 4 pins [form="♀ (female)"]

nets:
  N1: NANO.GND, Vin.pin1, Stepper.GND#14
  N2: NANO.D4, Stepper.DIR
  N3: NANO.D5, Stepper.STEP
  N4: NANO.D6, Stepper.ENABLE
  N5: NANO.D7, Stepper.MS1
  N6: NANO.D8, Stepper.MS2
  N7: NANO.D9, Stepper.MS3
  N8: NANO.D10, DREHENCODER.connector3
  N9: NANO.D11/MOSI, DREHENCODER.connector1
  N10: NANO.D12/MISO, DREHENCODER.connector4
  N11: NANO.VIN, Vin.pin2, Stepper.VMOT
  N12: NANO.A5, DISPLAY.pin4
  N13: NANO.A4, DISPLAY.pin3
  N14: NANO.A2, POTI.EncoderPinC
  N15: DREHENCODER.connector2, DREHENCODER.connector5, Stepper.GND#8
  N16: POTI.EncoderPinA, DISPLAY.pin2
  N17: POTI.EncoderPinB, DISPLAY.pin1
  N18: Stepper.RESET, Stepper.SLEEP
  N19: Stepper.1B, SteppOut.pin4
  N20: Stepper.1A, SteppOut.pin3
  N21: Stepper.2A, SteppOut.pin2
  N22: Stepper.2B, SteppOut.pin1
