# Fritzing sketch id3829_door_opener_0 (saved by Fritzing 0.9.3b)
breadboards: 1

parts:
  S1 = Ponte-H L298N
  Part1 = Arduino Nano (Rev3.0)
  Power_plug1 = Power plug [part_number=12v]  # not connected
  R1 = Photocell (LDR) [package=THT]
  R2 = Resistor [tolerance=±5% resistance=100k package=THT]
  M2 = DC Motor
  S2 = Toggle Switch [package=THT]
  R3 = Resistor [tolerance=±5% resistance=10k package=THT]

nets (from the schematic view):
  N1: S1.connector1, Part1.GND
  N2: S1.connector2, R2.Pin_0
  N3: S1.connector3, Part1.5V
  N4: S1.connector5, Part1.D3
  N5: S1.connector6, Part1.D2
  N6: S1.connector10, M2.pin_2
  N7: S1.connector11, S1.connector13, S1.connector14, S1.connector15, S1.connector16, M2.pin_1
  N8: Part1.D4, R3.Pin_1
  N9: Part1.A0, R1.pin_0, R2.Pin_1
  N10: R1.pin_1, S2.L2
  N11: S2.COM, R3.Pin_0
