# Fritzing sketch id3831_Slot_Car_PWM_Arduino_0 (saved by Fritzing 0.9.1b)
breadboards: 1

parts:
  Part1 = Arduino Uno (Rev3)
  D1 = Rectifier Diode [part_number=1N4001 package="300 mil [THT]"]  # not connected
  Q1 = Basic FET N-Channel [package="TO220 [THT]"]
  R1 = Resistor [tolerance=±5% resistance=220 package=THT]

nets:
  N1: Part1.D9_PWM, Q1.gate, R1.Pin_0
  N2: Part1.GND, Q1.source, R1.Pin_1
