# Fritzing sketch id3833_SpiegelreflexKamera_langzeitbelichtung_LCD_0 (saved by Fritzing 0.7.4b)
breadboards: 4

parts:
  U1 = atmega168 [package="DIP28 [THT]"]
  XTAL1 = Crystal [frequency="16 Mhz" package=THT]
  C1 = Ceramic Capacitor [capacitance=22pF voltage=6.3V package="100 mil [THT, multilayer]"]
  C2 = Ceramic Capacitor [capacitance=22pF package="100 mil [THT, multilayer]"]
  LCD1 = LCD screen
  TRS1 = Stereo Jack (TRS) 3.5mm [package="PG203J [THT]"]
  R1 = Rotary Potentiometer (Small) [maximum_resistance=100kΩ]
  VCC1 = Battery block 9V
  S1 = Pushbutton [package="[THT]"]
  S2 = Pushbutton [package="[THT]"]
  S3 = Pushbutton [package="[THT]"]
  S4 = Pushbutton [package="[THT]"]
  S5 = Pushbutton [package="[THT]"]
  S6 = Pushbutton [package="[THT]"]
  R2 = Resistor [tolerance=±5% resistance=10k package=THT]
  R3 = Resistor [tolerance=±5% resistance=10k package=THT]
  R4 = Resistor [tolerance=±5% resistance=10k package=THT]
  R5 = Resistor [tolerance=±5% resistance=10k package=THT]
  R6 = Resistor [tolerance=±5% resistance=10k package=THT]
  R7 = Resistor [tolerance=±5% resistance=10k package=THT]
  U2 = Voltage Regulator - 5V [package="TO220 [THT]"]
  C3 = Electrolytic Capacitor [capacitance=10µF package="100 mil [THT, electrolytic]"]
  D1 = Rectifier Diode [part_number=1N4001 package="300 mil [THT]"]
  C4 = Electrolytic Capacitor [capacitance=10µF package="100 mil [THT, electrolytic]"]
  R8 = Resistor [tolerance=±5% resistance=10k package=THT]
  S7 = Pushbutton [package="[THT]"]
  U3 = Optocoupler [package=THT]
  R9 = Resistor [tolerance=±5% resistance=680 package=THT]
  C5 = Ceramic Capacitor [capacitance=0.1µF package="100 mil [THT, multilayer]"]
  Q1 = NPN-Transistor [package="TO92 [THT]"]
  R10 = Resistor [tolerance=±5% resistance=1k package=THT]
  R11 = Resistor [tolerance=±5% resistance=10k package=THT]
  S8 = Pushbutton [package="[THT]"]
  R12 = Resistor [tolerance=±5% resistance=10k package=THT]

nets (from the schematic view):
  N1: U1.Pin_1, R8.Pin_0, S7.Pin_1, S7.Pin_2
  N2: U1.Pin_2, S5.Pin_3, S5.Pin_4, R6.Pin_1
  N3: U1.Pin_3, S6.Pin_3, S6.Pin_4, R7.Pin_1
  N4: U1.Pin_4, LCD1.DB7
  N5: U1.Pin_5, LCD1.DB6
  N6: U1.Pin_6, S1.Pin_3, S1.Pin_4, R2.Pin_1
  N7: U1.Pin_7, U1.Pin_20, LCD1.VDD, LCD1.LED+, R1.leg2, S1.Pin_1, S1.Pin_2, S2.Pin_1, S2.Pin_2, S3.Pin_1, S3.Pin_2, S4.Pin_1, S4.Pin_2, S5.Pin_1, S5.Pin_2, S6.Pin_1, S6.Pin_2, U2.output_voltage, C4.+, R8.Pin_1, C5.1, S8.Pin_1, S8.Pin_2
  VSS: U1.Pin_8, U1.Pin_22, C1.1, C2.0, LCD1.VSS, LCD1.R/W, R1.leg1, VCC1.-, R2.Pin_0, R3.Pin_0, R4.Pin_0, R5.Pin_0, R6.Pin_0, R7.Pin_0, U2.GND, C3.-, C4.-, S7.Pin_3, S7.Pin_4, R9.Pin_0, C5.0, Q1.E, R12.Pin_0
  N8: U1.Pin_9, XTAL1.pin_1, C1.0
  N9: U1.Pin_10, XTAL1.pin_0, C2.1
  N10: U1.Pin_11, S2.Pin_3, S2.Pin_4, R3.Pin_1
  N11: U1.Pin_12, S3.Pin_3, S3.Pin_4, R4.Pin_1
  N12: U1.Pin_13, R11.Pin_0
  N13: U1.Pin_14, S4.Pin_3, S4.Pin_4, R5.Pin_1
  N14: U1.Pin_15, LCD1.DB5
  N15: U1.Pin_16, LCD1.DB4
  N16: U1.Pin_17, LCD1.E
  N17: U1.Pin_18, LCD1.RS
  N18: U1.Pin_19, U3.Pin_1
  N19: U1.Pin_23, S8.Pin_3, S8.Pin_4, R12.Pin_1
  N20: LCD1.V0, R1.wiper
  N21: LCD1.LED-, R10.Pin_1
  N22: TRS1.Sleeve, U3.Pin_4
  N23: TRS1.Tip, U3.Pin_5
  N24: VCC1.+, D1.anode
  N25: U2.input_voltage, C3.+, D1.cathode
  N26: U3.Pin_2, R9.Pin_1
  N27: Q1.B, R11.Pin_1
  N28: Q1.C, R10.Pin_0

notes:
  Shot + - A1 A2 A3
