# Fritzing sketch id3834_One_SMA_drive_circuit_0 (saved by Fritzing 0.9.3b)
breadboards: 1

parts:
  パーツ1 = Arduino Uno (Rev3)
  L1 = Inductor [package="1206 [SMD]"]
  R1 = Resistor [tolerance=±5% resistance=1.5k package="0603 [SMD]"]
  Q1 = MOSFET-NCHANNEL [package=to220v]

nets:
  N1: パーツ1.D3_PWM, R1.Pin_1
  N2: パーツ1.GND, Q1.S
  N3: パーツ1.VIN, L1.pin_1
  N4: L1.pin_0, Q1.D
  N5: R1.Pin_0, Q1.G
