# Fritzing sketch id3836_DMX_Control_Desk_micro_1v1_1_0 (saved by Fritzing 0.9.2b)
circuit board: 7.10464cm x 5.73832cm
breadboards: 1

parts:
  Part1 = Arduino Micro (Rev3)
  J1 = Power Jack [package=power_jack_pth]
  JP1 = Header 12 [package=1x12_machine-pin-header_lock.004]
  JP2 = Header 12 [package=1x12_machine-pin-header_lock.004]
  JP3 = Header 12 [package=1x12_machine-pin-header_lock.004]
  IC1 = IC, DIP package, 8 pins [chip_label=6n137]
  J2 = female pin header, 4 pins [form="♀ (female)"]
  XLR = female pin header, 3 pins [form="♀ (female)" part_number=XLR]
  R1 = Resistor [tolerance=±5% resistance=10k package="0805 [SMD]"]
  XLR1 = XLR3_NCFAH2 [package=xlr3_nc3fah2]
  7_seg = female pin header, 5 pins [form="♀ (female)"]
  C1 = Ceramic Capacitor [capacitance=1µF voltage=10V package="0805 [SMD, multilayer]"]
  sw2 = female pin header, 3 pins [form="♀ (female)"]
  sw1 = female pin header, 3 pins [form="♀ (female)"]
  IC2 = IC, DIP package, 8 pins [chip_label=SN75176BP]
  R2 = Resistor [tolerance=±5% resistance=2.2k package="0805 [SMD]"]

nets:
  GND: Part1.GND, J1.GND, J1.GNDBREAK, JP2.1, JP2.2, JP2.3, JP2.4, JP2.5, JP2.6, JP2.7, JP2.8, JP2.9, JP2.10, JP2.11, JP2.12, J2.pin4, 7_seg.pin1, sw2.pin2, sw1.pin2
  N1: Part1.D2/SDA, sw1.pin1
  N2: Part1.D3/SCL, sw2.pin1
  N3: Part1.D4_PWM/A6, JP3.7
  N4: Part1.D5_PWM, 7_seg.pin4
  N5: Part1.D6_PWM/A7, JP3.8
  N6: Part1.D7, 7_seg.pin3
  N7: Part1.D8_PWM/A8, JP3.9
  N8: Part1.D9_PWM/A9, JP3.10
  N9: Part1.D10_PWM/A10, JP3.11
  N10: Part1.D11_PWM, 7_seg.pin2
  N11: Part1.D12_PWM/A11, JP3.12
  N12: Part1.VIN, J1.PWR
  N13: Part1.5V, JP1.1, JP1.2, JP1.3, JP1.4, JP1.5, JP1.6, JP1.7, JP1.8, JP1.9, JP1.10, JP1.11, JP1.12, IC1.pin2, J2.pin3, 7_seg.pin5, sw2.pin3, sw1.pin3
  N14: Part1.A5, JP3.6
  N15: Part1.A4, JP3.5
  N16: Part1.A3, JP3.4
  N17: Part1.A2, JP3.3
  N18: Part1.A1, JP3.2
  N19: Part1.A0, JP3.1
  N20: Part1.D13_PWM, R2.Pin_1
  N21: IC1.pin3, R2.Pin_0
  N22: IC1.pin5, J2.pin2, XLR.pin3, XLR1.1, XLR1.G, C1.1, IC2.pin5
  N23: IC1.pin6, R1.Pin_1, IC2.pin4
  N24: IC1.pin8, J2.pin1, R1.Pin_0, C1.0, IC2.pin2, IC2.pin3, IC2.pin8
  N25: XLR.pin1, XLR1.3, IC2.pin6
  N26: XLR.pin2, XLR1.2, IC2.pin7

notes:
  DMX Control Desk
  v 1.1
  .
