# Fritzing sketch id3839_Small_Led_Light_0 (saved by Fritzing 0.9.3b)
circuit board: 2.42548cm x 0.957512cm
breadboards: 1

parts:
  R1 = Resistor [tolerance=±5% resistance=220 package=THT]
  LED1 = LED - 5mm [color="Red (633nm)" package="5 mm [THT]"]
  VCC1 = Battery
  S1 = Toggle Switch [package=THT]

nets:
  N1: R1.Pin_0, VCC1.-
  N2: R1.Pin_1, LED1.anode
  N3: LED1.cathode, S1.COM
  N4: VCC1.+, S1.L1
