# Fritzing sketch id383_analog_buttons__0 (saved by Fritzing 0.9.0b)
circuit board: 4.72551cm x 2.46721cm
perfboards: 1

parts:
  S1 = Pushbutton [package="[THT]"]
  S2 = Pushbutton [package="[THT]"]
  S3 = Pushbutton [package="[THT]"]
  S4 = Pushbutton [package="[THT]"]
  S5 = Pushbutton [package="[THT]"]
  R1 = Resistor [tolerance=±5% resistance=2k package=THT]
  R2 = Resistor [tolerance=±5% resistance=330 package=THT]
  R3 = Resistor [tolerance=±5% resistance=470 package=THT]
  R4 = Resistor [tolerance=±5% resistance=3.3k package=THT]
  R5 = Resistor [tolerance=±5% resistance=1k package=THT]
  JP2 = Header 3 [package=molex-1x3_lock]

nets:
  N1: S1.Pin_1, S1.Pin_2, S2.Pin_1, S2.Pin_2, S3.Pin_1, S3.Pin_2, S4.Pin_1, S4.Pin_2, S5.Pin_1, S5.Pin_2, JP2.1
  N2: S1.Pin_3, S1.Pin_4, R4.Pin_1
  N3: S2.Pin_3, S2.Pin_4, R1.Pin_0, R2.Pin_1, JP2.3
  N4: S3.Pin_3, S3.Pin_4, R2.Pin_0, R3.Pin_0
  N5: S4.Pin_3, S4.Pin_4, R3.Pin_1, R5.Pin_0
  N6: S5.Pin_3, S5.Pin_4, R4.Pin_0, R5.Pin_1
  N7: R1.Pin_1, JP2.2

notes:
  GND
  +5V
  OUT
