# Fritzing sketch id3841_Robot (saved by Fritzing 0.9.3b)
breadboards: 1

parts:
  hc-sr1 = hc-sr04
  J1 = Basic Servo
  J2 = Basic Servo
  Часть1 = Arduino Uno (Rev3)
  S1 = Ponte-H L298N
  M1 = DC Motor
  M2 = DC Motor  # not connected
  J3 = Infrared Proximity Sensor

nets:
  VCC: hc-sr1.VCC, J2.vcc, Часть1.5V, J3.Vcc
  N1: hc-sr1.Trig, Часть1.D8
  N2: hc-sr1.Echo, Часть1.D9_PWM
  GND: hc-sr1.GND, J2.gnd, Часть1.GND, S1.connector1, J3.GND
  N3: J1.pulse, Часть1.D10_PWM/SS
  N4: Часть1.D11_PWM/MOSI, J3.Vout
  N5: Часть1.D2, S1.connector3
  N6: Часть1.D4, S1.connector4
  N7: Часть1.D5_PWM, S1.connector5
  N8: Часть1.D7, S1.connector6
  N9: S1.connector8, M1.pin_1

notes:
  ENA подключить к пину D6,
  ENB подключить к пину D3
