# Fritzing sketch id3841_nixieclock_small_0 (saved by Fritzing 0.9.2b)
circuit board: 9.65cm x 7.86493cm
breadboards: 1

parts:
  Arduino = Arduino Nano (Rev3.0)
  J8 = female pin header, 1 pin [form="♀ (female)"]  # not connected
  Power = male pin header, 2 pins [form="♂ (male)"]
  RTC = female pin header, 4 pins [form="♀ (female)"]
  BT = female pin header, 4 pins [form="♀ (female)"]
  J11 = female pin header, 1 pin [form="♀ (female)"]
  J6 = female pin header, 8 pins [form="♀ (female)"]  # not connected
  J9 = female pin header, 2 pins [form="♀ (female)"]  # not connected
  J7 = female pin header, 3 pins [form="♀ (female)"]  # not connected
  R1 = Resistor [tolerance=±5% resistance=3.3 package=THT]
  R2 = Resistor [tolerance=±5% resistance=3.3k package=THT]
  R3 = Resistor [tolerance=±5% resistance=3.3k package=THT]
  Q1 = NPN-Transistor [package="TO92 [THT]"]
  Q2 = NPN-Transistor [package="TO92 [THT]"]
  Q3 = NPN-Transistor [package="TO92 [THT]"]
  R4 = Resistor [tolerance=±5% resistance=3.3k package=THT]
  R5 = Resistor [tolerance=±5% resistance=3.3k package=THT]
  R6 = Resistor [tolerance=±5% resistance=3.3k package=THT]
  Q4 = NPN-Transistor [package="TO92 [THT]"]
  Q5 = NPN-Transistor [package="TO92 [THT]"]
  Q6 = NPN-Transistor [package="TO92 [THT]"]
  R10 = Resistor [tolerance=±5% resistance=3.3k package=THT]
  R11 = Resistor [tolerance=±5% resistance=3.3k package=THT]
  R12 = Resistor [tolerance=±5% resistance=3.3k package=THT]
  R7 = Resistor [tolerance=±5% resistance=3.3k package=THT]
  R8 = Resistor [tolerance=±5% resistance=3.3k package=THT]
  R9 = Resistor [tolerance=±5% resistance=3.3k package=THT]
  J4 = female pin header, 3 pins [form="♀ (female)"]
  J2 = female pin header, 2 pins [form="♀ (female)"]
  J5 = male pin header, 8 pins [form="♂ (male)"]  # not connected
  IC1 = Voltage Regulator [package=to-220-alt]

nets:
  N1: Arduino.D5, RTC.pin4
  N2: Arduino.D6, RTC.pin3
  N3: Arduino.D11/MOSI, RTC.pin2, BT.pin3, J2.pin1
  N4: Arduino.D12/MISO, RTC.pin1, J11.pin1, IC1.IN
  N5: Arduino.VIN, R1.Pin_0
  N6: Arduino.GND, R2.Pin_0
  N7: Arduino.RESET, R3.Pin_0
  N8: Arduino.3V3, BT.pin2
  N9: Arduino.D13/SCK, BT.pin1
  N10: Power.pin1, IC1.OUT
  N11: Power.pin2, IC1.GND
  N12: R1.Pin_1, Q1.B
  N13: R2.Pin_1, Q2.B
  N14: R3.Pin_1, Q3.B
  N15: Q1.C, R4.Pin_0
  N16: Q2.C, R5.Pin_0
  N17: Q3.C, R6.Pin_0
  N18: R4.Pin_1, Q4.E, Q4.B, R10.Pin_1
  N19: R5.Pin_1, Q5.B, R11.Pin_1
  N20: R6.Pin_1, Q6.B, R12.Pin_1
  N21: Q4.C, J4.pin1
  N22: Q5.E, R11.Pin_0, R8.Pin_0
  N23: Q5.C, J4.pin2
  N24: Q6.E, R12.Pin_0, R9.Pin_0
  N25: Q6.C, J4.pin3
  N26: R10.Pin_0, R7.Pin_0
  N27: R7.Pin_1, R8.Pin_1, R9.Pin_1, J2.pin2
