# Fritzing sketch id3845_Untitled_Sketch_0 (saved by Fritzing 0.8.7b)
circuit board: 8.46667cm x 5.64444cm
breadboards: 1

parts:
  U3 = SWITCH_SPDT [package=kps-1290]
  M1 = DC Motor  # not connected
  M2 = DC Motor  # not connected
  Часть1 = Arduino Uno (Rev3)
  Часть3 = Rotoshield - Motor driver shield for Arduino
  VCC1 = 4 x AAA Battery Mount
  U4 = IRRECEIVER [package=tsop8523]
  U6 = IRRECEIVER [package=tsop8523]

nets:
  N1: U3.O, VCC1.+
  5V: U3.P, Часть1.5V, Часть3.+5V, U4.VS, U6.VS
  N2: Часть1.D8, U6.OUT
  N3: Часть1.D9_PWM, U4.OUT
  GND: Часть1.GND, Часть3.GND, VCC1.-
  N4: Часть1.D2, Часть3.A_IN_2
  N5: Часть1.D3_PWM, Часть3.A_IN_1
  N6: Часть1.D4, Часть3.A_IN_4
  N7: Часть1.D5_PWM, Часть3.A_IN_3
  N8: Часть1.D6_PWM, Часть3.A_IN_5
  GND_2: U4.GND, U6.GND

notes:
  Poteruha V.
  Vasin D.
  Minsk, 2014
