# Fritzing sketch id3846_Smart_Door_0 (saved by Fritzing 0.9.3b)
breadboards: 1

parts:
  Componente1 = Arduino Uno (Rev3)
  U1 = LCD-16X2 [package=lcd-16x2_noholes]
  Matrix_keypad1 = CMG
  U2 = POT [package=pot_alpha_rv16af-20]
  servo = Basic Servo
  S1 = Pushbutton [package="[THT]"]
  S2 = Pushbutton [package="[THT]"]
  R1 = Resistor [tolerance=±5% resistance=220 package=THT]
  R2 = Resistor [tolerance=±5% resistance=220 package=THT]

nets:
  N1: Componente1.A0, servo.pulse
  N2: Componente1.A1, Matrix_keypad1.connector31
  N3: Componente1.A2, Matrix_keypad1.connector32
  N4: Componente1.A3, U1.RS
  N5: Componente1.A4/SDA, U1.E
  N6: Componente1.D8, U1.DB7
  N7: Componente1.D9_PWM, U1.DB6
  N8: Componente1.D10_PWM/SS, U1.DB5
  N9: Componente1.D11_PWM/MOSI, U1.DB4
  N10: Componente1.D12/MISO, S1.Pin_3, S1.Pin_4, R2.Pin_0
  N11: Componente1.D13/SCK, S2.Pin_3
  N12: Componente1.D2, Matrix_keypad1.connector30
  N13: Componente1.D3_PWM, Matrix_keypad1.connector29
  N14: Componente1.D4, Matrix_keypad1.connector28
  N15: Componente1.D5_PWM, Matrix_keypad1.connector27
  N16: Componente1.D6_PWM, Matrix_keypad1.connector26
  N17: Componente1.D7, Matrix_keypad1.connector25
  5V: Componente1.5V, U1.VDD, U1.A, U2.E, servo.vcc
  GND: Componente1.GND, U1.VSS, U1.R_W, U1.K, U2.A, R1.Pin_1, R2.Pin_1
  N18: U1.VO, U2.S
