# Fritzing sketch id3847_home_0 (saved by Fritzing 0.9.0b)
breadboards: 1

parts:
  Part1 = prefix101251
  DHT1 = DHT11_Temperature_and_Humitidy_Sensor
  R1 = Photocell (LDR) [package=THT]
  Part2 = Arduino Uno (Rev3)
  R2 = Resistor [tolerance=±5% resistance=220 package=THT]
  LED1 = smd LED [color="Red (633nm)" package="0603 [SMD]"]
  R3 = Resistor [tolerance=±5% resistance=220 package=THT]

nets:
  N1: Part1.connector5, DHT1.connector4, Part2.GND, R2.Pin_1, LED1.cathode
  N2: Part1.connector6, Part2.A1
  N3: Part1.connector10, DHT1.connector1, R1.pin_0, Part2.5V
  N4: DHT1.connector2, Part2.A0
  N5: R1.pin_1, Part2.D2, R2.Pin_0
  N6: Part2.D3_PWM, R3.Pin_1
  N7: LED1.anode, R3.Pin_0
