# Fritzing sketch id3848_Attiny85_CaricabatterieDef_0 (saved by Fritzing 0.7.4b)

parts:
  R1 = Resistor [tolerance=±5% resistance=15k package=THT]
  R2 = Resistor [tolerance=±5% resistance=33k package=THT]
  Power_plug1 = Power plug
  Q1 = NPN-Transistor [part_number=BC547 package="TO92 [THT]"]
  R3 = Resistor [tolerance=±5% resistance=2k package=THT]
  R4 = Resistor [tolerance=±5% resistance=470 package=THT]
  R5 = Resistor [tolerance=±5% resistance=0.3 power=2W package=THT]
  Attiny85 = attiny85
  CHARGE = LED - 3mm [color="Red (635nm)" package="3 mm [THT]"]
  Q2 = pnp-Powertransistor [part_number=TIP127 package="TO220 [THT]"]
  J1 = male pin header, 3 pins [form="♂ (male)"]
  J2 = male pin header, 3 pins [form="♂ (male)"]
  J1_2 = female pin header, 2 pins [form="♀ (female)"]
  C1 = Ceramic Capacitor [capacitance=100nF package="100 mil [THT, multilayer]"]
  C2 = Ceramic Capacitor [capacitance=10nF package="100 mil [THT, multilayer]"]
  PWR = LED - 3mm [color="Green (560nm)" package="3 mm [THT]"]
  R6 = Resistor [tolerance=±5% resistance=5k package=THT]
  vreg = Voltage Regulator - 5V [package="TO220 [THT]"]
  BATT = Screw terminal - 2 pins [package=THT]
  debug = female pin header, 2 pins [form="♀ (female)"]
  D1 = Schottky Diode [part_number=1N5822 package="300 mil [THT]"]

nets:
  GND: R1.Pin_0, Power_plug1.GND, Q1.E, Attiny85.connector3, J2.pin1, C1.0, C2.0, PWR.cathode, vreg.GND, BATT.pin1, debug.pin2
  N1: R1.Pin_1, R2.Pin_1, Attiny85.connector6, J1.pin2
  N2: R2.Pin_0, BATT.pin2, D1.cathode
  N3: Power_plug1.VCC, R5.Pin_1, CHARGE.anode, C1.1, R6.Pin_0, vreg.input_voltage
  N4: Q1.B, R3.Pin_1
  N5: Q1.C, R4.Pin_1
  N6: R3.Pin_0, J1_2.pin1
  N7: R4.Pin_0, CHARGE.cathode, Q2.base
  N8: R5.Pin_0, Q2.emitter
  N9: Attiny85.connector0, J1.pin3
  N10: Attiny85.connector1, debug.pin1
  N11: Attiny85.connector4, J2.pin2, J1_2.pin2
  N12: Attiny85.connector5, J1.pin1
  N13: Attiny85.connector7, J2.pin3, C2.1, vreg.output_voltage
  N14: Q2.collector, D1.anode
  N15: PWR.anode, R6.Pin_1

notes:
  +
  -
  ICSP
  NiMh Charger 0.9
  by Toggio
  red
  2012
