# Fritzing sketch id3849_smartparking_0 (saved by Fritzing 0.9.2b)
breadboards: 1

parts:
  J1 = Infrared Proximity Sensor
  J3 = Infrared Proximity Sensor
  J4 = Infrared Proximity Sensor
  Part1 = Arduino Ethernet Shield (Rev3)  # not connected

nets:
  GND: J1.GND, J3.GND, J4.GND
  VCC: J1.Vcc, J3.Vcc, J4.Vcc
