# Fritzing sketch id384_12_14V_car_power_supply_converter_0 (saved by Fritzing 0.7.11b)
breadboards: 1

parts:
  Fuse2 = Fuse with Handler [part_number="3A slow-blow fuse"]
  R3 = Resistor [tolerance=±5% resistance=100k package=THT]
  D3 = Rectifier Diode [part_number=1N4001 package="300 mil [THT]"]
  R4 = Resistor [tolerance=±5% resistance=47k package=THT]
  D4 = Zener Diode [part_number=5,6V breakdown_voltage=5.1V package="300 mil [THT]"]
  Arduino2 = Arduino
  U2 = Voltage Regulator - 5V [part_number=LM2940CT-5 package="TO220 [THT]"]
  C4 = Electrolytic Capacitor [capacitance=4.7mF voltage=16V package="300 mil [THT, electrolytic]"]
  C5 = Electrolytic Capacitor [capacitance=4.7µF package="100 mil [THT, electrolytic]"]
  C6 = Ceramic Capacitor [capacitance=100nF package="200 mil [THT, multilayer]"]
  J3 = Screw terminal - 2 pins [part_number="To Arduino" package=THT]
  J4 = Screw terminal - 2 pins [part_number="From car power supply" package=THT]
  J5 = Generic female header - metal rounded [package=THT]
  J6 = Generic male header [package=THT]

nets:
  N1: Fuse2.Connector1, J4.pin2
  N2: Fuse2.Connector2, R3.Pin_0, D3.anode
  N3: R3.Pin_1, R4.Pin_0, D4.cathode, Arduino2.D3, J5.pin1, J6.pin1
  N4: D3.cathode, U2.input_voltage, C4.+
  N5: R4.Pin_1, D4.anode, U2.GND, C4.-, C5.-, C6.0, J3.pin2, J4.pin1
  N6: U2.output_voltage, C5.+, C6.1, J3.pin1
