# Fritzing sketch id3850_PillBox_prototype_0 (saved by Fritzing 0.7.12b)
perfboards: 1
breadboards: 2

parts:
  Arduino1 = Arduino
  LED1 = LED - 5mm [color="Blue (470nm)" package="5 mm [THT]"]
  LED2 = LED - 5mm [color="Blue (470nm)" package="5 mm [THT]"]
  LED5 = LED - 5mm [color="Blue (470nm)" package="5 mm [THT]"]
  LED6 = LED - 5mm [color="Blue (470nm)" package="5 mm [THT]"]
  LED7 = LED - 5mm [color="Blue (470nm)" package="5 mm [THT]"]
  LED8 = LED - 5mm [color="Blue (470nm)" package="5 mm [THT]"]
  LED9 = LED - 5mm [color="Blue (470nm)" package="5 mm [THT]"]
  R2 = Resistor [tolerance=±5% resistance=330 package=THT]
  R3 = Resistor [tolerance=±5% resistance=330 package=THT]
  R4 = Resistor [tolerance=±5% resistance=330 package=THT]
  R5 = Resistor [tolerance=±5% resistance=330 package=THT]
  R6 = Resistor [tolerance=±5% resistance=330 package=THT]
  R7 = Resistor [tolerance=±5% resistance=330 package=THT]
  R8 = Resistor [tolerance=±5% resistance=330 package=THT]
  LED10 = LED - 5mm [color="White (8000K)" package="5 mm [THT]"]
  LED11 = LED - 5mm [color="White (8000K)" package="5 mm [THT]"]
  LED12 = LED - 5mm [color="White (8000K)" package="5 mm [THT]"]
  LED13 = LED - 5mm [color="White (8000K)" package="5 mm [THT]"]
  LED14 = LED - 5mm [color="White (8000K)" package="5 mm [THT]"]
  LED15 = LED - 5mm [color="White (8000K)" package="5 mm [THT]"]
  LED16 = LED - 5mm [color="White (8000K)" package="5 mm [THT]"]
  R9 = Resistor [tolerance=±5% resistance=10k package=THT]
  R11 = Resistor [tolerance=±5% resistance=10k package=THT]
  R12 = Resistor [tolerance=±5% resistance=10k package=THT]
  R13 = Resistor [tolerance=±5% resistance=10k package=THT]
  R14 = Resistor [tolerance=±5% resistance=10k package=THT]
  R15 = Resistor [tolerance=±5% resistance=10k package=THT]
  R16 = Resistor [tolerance=±5% resistance=10k package=THT]

nets:
  N1: Arduino1.D2, R2.Pin_1, R3.Pin_1, R4.Pin_1, R5.Pin_1, R6.Pin_1, R7.Pin_1, R8.Pin_1
  N2: Arduino1.+5V, LED11.cathode, LED12.cathode, LED13.cathode, LED14.cathode, LED15.cathode, LED16.cathode
  N3: Arduino1.GND, LED1.anode, LED2.anode, LED5.anode, LED6.anode, LED7.anode, LED8.anode, LED9.anode, R9.Pin_1, R11.Pin_1, R12.Pin_1, R13.Pin_1, R14.Pin_1, R15.Pin_1, R16.Pin_1
  N4: Arduino1.A0, LED10.anode, R9.Pin_0
  N5: Arduino1.A1, LED11.anode, R11.Pin_0
  N6: Arduino1.A2, LED12.anode, R12.Pin_0
  N7: Arduino1.A3, LED13.anode, R14.Pin_0
  N8: Arduino1.A4, LED14.anode, R13.Pin_0
  N9: Arduino1.A5, LED15.anode, R16.Pin_0
  N10: LED1.cathode, R2.Pin_0
  N11: LED2.cathode, R3.Pin_0
  N12: LED5.cathode, R4.Pin_0
  N13: LED6.cathode, R6.Pin_0
  N14: LED7.cathode, R5.Pin_0
  N15: LED8.cathode, R8.Pin_0
  N16: LED9.cathode, R7.Pin_0
  N17: LED16.anode, R15.Pin_0
