# Fritzing sketch id3851_stem_project_0 (saved by Fritzing 0.9.2b)
breadboards: 1

parts:
  Part1 = Arduino Uno (Rev3)
  J1 = Basic Force Sensing Resistor (FSR) [package=THT]
  R1 = Resistor [tolerance=±5% resistance=220 package=THT]
  R2 = Resistor [tolerance=±5% resistance=220 package=THT]
  R3 = Resistor [tolerance=±5% resistance=220 package=THT]
  U1 = TEMPERATURE-SENSOR [package=to-92]
  U2 = TEMPERATURE-SENSOR [package=to-92]
  J2 = Peltier Element
  J3 = Peltier Element
  U3 = L298 [package=multiwatt15_6400bgheatsink]
  VCC1 = prefix0000

nets:
  N1: Part1.A2, R1.Pin_1
  GND: Part1.GND, J1.pin_1, U1.GND, U2.GND, U3.GND, VCC1.connector0
  N2: Part1.D2, R2.Pin_1, U1.ADJ
  N3: Part1.D3_PWM, R3.Pin_0, U2.ADJ
  N4: Part1.D6_PWM, U3.VS
  N5: Part1.D7, U3.ENA
  VCC: Part1.5V, J1.pin_0, R1.Pin_0, R2.Pin_0, R3.Pin_1, U1.VCC, U2.VCC, U3.IN1
  N6: J2.pin1, J3.pin1, U3.OUT1
  N7: J2.pin2, J3.pin2, U3.OUT2
  N8: U3.IN2, VCC1.connector1
