# Fritzing sketch id3853_Smartwardrobe_0 (saved by Fritzing 0.9.2b)

parts:
  UHF_RFID1 = uhf-rfid-jt2850
  Part1 = Arduino Uno (Rev3)

nets:
  N1: UHF_RFID1.connector2, Part1.GND
  N2: UHF_RFID1.connector2pin_4, Part1.D0/RX
  N3: UHF_RFID1.connector2pin_5, Part1.D1/TX
  N4: UHF_RFID1.connector2pin_10, Part1.5V

notes:
  Antenna is connected
  Arduino communicate with Raspberry Pi2 through USB port
