# Fritzing sketch id3854_main_SMART_0 (saved by Fritzing 0.9.2b)
circuit board: 8.84854cm x 6.30767cm
breadboards: 2

parts:
  Part1 = Arduino Yun
  R1 = Resistor [tolerance=±5% resistance=4.7k package=THT]
  R2 = Resistor [tolerance=±5% resistance=4.7k package=THT]
  C1 = Ceramic Capacitor [capacitance=100nF package="100 mil [THT, multilayer]"]
  DHT22 = Humidity and Temperature Sensor RHT03
  R3 = Resistor [tolerance=±5% resistance=10k package=THT]
  LIDAR = Humidity and Temperature Sensor RHT03
  MLX = Humidity and Temperature Sensor RHT03
  Halfservo = Basic Servo
  Motor = Basic Servo
  U1 = RELAY [package=relay-t9a-2]

nets:
  N1: Part1.A4/SDA, R1.Pin_1, LIDAR.GND_1, MLX.GND_1
  N2: Part1.A5/SCL, R2.Pin_1, LIDAR.Data-signal, MLX.Data-signal
  VCC: Part1.5V, R1.Pin_0, R2.Pin_0, C1.1, DHT22.Vcc, R3.Pin_0, LIDAR.Vcc, MLX.Vcc, Halfservo.vcc, Motor.vcc, U1.COIL1
  GND: Part1.GND, C1.0, DHT22.GND_2, LIDAR.GND_2, MLX.GND_2, Halfservo.gnd, Motor.gnd, U1.COIL2
  N3: Part1.D0/RX, Halfservo.pulse
  N4: Part1.D1/TX, U1.NC
  N5: Part1.D2, DHT22.Data-signal, R3.Pin_1
  N6: Part1.D7, U1.MAIN
  N7: Motor.pulse, U1.NO
