# Fritzing sketch id3855_1_0 (saved by Fritzing 0.9.2b)
breadboards: 1

parts:
  Part1 = Triple Axis Accelerometer Breakout - ADXL335
  Part2 = Triple Axis Accelerometer Breakout - ADXL335
  Part3 = Bluetooth HC-05 Macho
  Part4 = Arduino Nano (Rev3.0)
  Part5 = Triple Axis Accelerometer Breakout - ADXL345

nets:
  N1: Part1.ZOUT, Part4.A5
  N2: Part1.YOUT, Part4.A6
  N3: Part1.XOUT, Part4.A7
  GND: Part1.GND, Part2.GND, Part3.GND, Part4.GND, Part5.GND
  VCC: Part1.VCC, Part3.VCC, Part4.3V3, Part5.VCC, Part5.CS
  N4: Part2.ZOUT, Part4.A2
  N5: Part2.YOUT, Part4.A3
  N6: Part2.XOUT, Part4.A4
  N7: Part3.TXD, Part4.D11/MOSI
  N8: Part3.RXD, Part4.D10
  N9: Part4.A1, Part5.SCL
  N10: Part4.A0, Part5.SDA
