# Fritzing sketch id3856_Untitled_Sketch_0 (saved by Fritzing 0.9.1b)
breadboards: 1

parts:
  Parte1 = Arduino Uno (Rev3)
  Raspberry_Pi_B_rev1 = Raspberry Pi B rev1
  RHT1 = Humidity and Temperature Sensor RHT03
  LED1 = RGB LED - (4 legs) [package="5 mm [THT]"]
  LED2 = LEDs [package=led10mm]
  LED3 = LEDs [package=led10mm]
  LED4 = LEDs [package=led10mm]
  LED5 = LEDs [package=led10mm]
  LED6 = LEDs [package=led10mm]
  LED7 = LEDs [package=led10mm]
  LED8 = LEDs [package=led10mm]
  LED9 = LEDs [package=led10mm]
  R1 = Resistor [tolerance=±5% resistance=220 package=THT]
  R2 = Photocell (LDR) [package=THT]

nets:
  N1: Parte1.A2, R1.Pin_1, R2.pin_0
  N2: Parte1.D9_PWM, LED1.blue_cathode
  N3: Parte1.D10_PWM/SS, LED1.green_cathode
  N4: Parte1.D11_PWM/MOSI, LED1.red_cathode
  N5: Parte1.D2, LED2.C, LED5.C
  N6: Parte1.D3_PWM, LED3.C, LED4.C
  N7: Parte1.D4, LED7.C, LED8.C
  N8: Parte1.D5_PWM, LED6.C, LED9.C
  3V3: Parte1.3V3, RHT1.Vcc
  N9: Parte1.GND, LED1.common_anode, LED2.A, LED3.A, LED4.A, LED5.A, LED6.A, LED7.A, LED8.A, LED9.A, R1.Pin_0, R2.pin_1
  N10: Raspberry_Pi_B_rev1.GPIO_1, Raspberry_Pi_B_rev1.GPIO_4, RHT1.Data-signal
  N11: Raspberry_Pi_B_rev1.GND, RHT1.GND_2

notes:
  3.3 Volts
  5 Volts
  Luces Exteriores
  Luces Interiores
  LED RGB Controlador ->
