# Fritzing sketch id3859_Untitled_Sketch_2_0 (saved by Fritzing 0.9.2b)
breadboards: 1

parts:
  Part1 = Arduino Uno (Rev3)
  Part2 = Bluetooth Mate Silver
  R1 = Resistor [tolerance=±5% resistance=10 package=THT]
  R2 = Resistor [tolerance=±5% resistance=10 package=THT]
  R3 = Resistor [tolerance=±5% resistance=10 package=THT]
  Part3 = Triple Axis Accelerometer Breakout - ADXL335
  U1 = mystery part, 3 pins [chip_label=WeightSensor]

nets:
  N1: Part1.A0, U1.pin1
  N2: Part1.A1, Part3.XOUT
  N3: Part1.A2, Part3.YOUT
  N4: Part1.A3, Part3.ZOUT
  GND: Part1.GND, Part2.GND, R3.Pin_1, Part3.GND, U1.pin3
  N5: Part1.D0/RX, Part2.TX_5V
  N6: Part1.D1/TX, R1.Pin_0
  VCC: Part1.3V3, Part2.VCC, Part3.VCC, U1.pin2
  N7: Part2.RX_5V, R1.Pin_1, R2.Pin_0
  N8: R2.Pin_1, R3.Pin_0
