# Fritzing sketch id385_MultiLEDsMiniBreadboard_0 (saved by Fritzing 0.7.11b)
breadboards: 1

parts:
  LED1 = LED - 5mm [color="Red (633nm)" package="5 mm [THT]"]
  R1 = Resistor [tolerance=±5% resistance=150 package=THT]
  LED2 = LED - 5mm [color="Red (633nm)" package="5 mm [THT]"]
  R2 = Resistor [tolerance=±5% resistance=150 package=THT]
  LED3 = LED - 5mm [color="Yellow (574nm)" package="5 mm [THT]"]
  R3 = Resistor [tolerance=±5% resistance=150 package=THT]
  LED4 = LED - 5mm [color="Yellow (574nm)" package="5 mm [THT]"]
  R4 = Resistor [tolerance=±5% resistance=150 package=THT]
  LED5 = LED - 5mm [color="Red (633nm)" package="5 mm [THT]"]
  R5 = Resistor [tolerance=±5% resistance=150 package=THT]
  LED6 = LED - 5mm [color="Red (633nm)" package="5 mm [THT]"]
  R6 = Resistor [tolerance=±5% resistance=150 package=THT]
  Arduino1 = Arduino

nets:
  N1: LED1.cathode, R1.Pin_0
  N2: LED1.anode, LED2.anode, LED3.anode, LED4.anode, LED5.anode, LED6.anode, Arduino1.+5V
  N3: R1.Pin_1, Arduino1.D2
  N4: LED2.cathode, R2.Pin_0
  N5: R2.Pin_1, Arduino1.D4
  N6: LED3.cathode, R3.Pin_0
  N7: R3.Pin_1, Arduino1.D6
  N8: LED4.cathode, R4.Pin_1
  N9: R4.Pin_0, Arduino1.D7
  N10: LED5.cathode, R5.Pin_1
  N11: R5.Pin_0, Arduino1.D5
  N12: LED6.cathode, R6.Pin_1
  N13: R6.Pin_0, Arduino1.D3

notes:
  Six LEDs on a Mini Breadboard
  The breadboard has 17 columns and 2 x 5 rows
  There is a break between rows 5 and 6
  The anode wires from the LEDs are all in a column
  Column 1 on the left and column 17 on the right
  The cathode wires bend out to attach each to a
  150 ohm resistor (I don't have any 220s).
  A data wire runs from each resistor to a digital
  pin on the Arduino from 2 through 7
  The 5v power goes to column 1(5), then a wire
  runs it from 1(1) to 1(10), then another wire takes
  it from 1(10) to 10(10), then another wires takes
  it from 10(6) to 10(1) to feed the whole 2 columns 1 and 10
  MultiLEDs
  Derek Erb - 26/01/2013
  about.me/derekerb
  derek.erb@gmail.com
