# Fritzing sketch id3860_bluetooth_rover_0 (saved by Fritzing 0.9.3b)

parts:
  S1 = Ponte-H L298N
  Part1 = Bluetooth HC-05 Macho
  Part2 = Arduino Uno (Rev3)
  M1 = DC Motor
  VCC1 = Battery
  VCC2 = Battery block 9V  # not connected
  S2 = Toggle Switch [package=THT]
  M2 = DC Motor

nets:
  N1: S1.connector0, S2.COM
  GND: S1.connector1, Part1.GND, Part2.GND, VCC1.-
  N2: S1.connector3, Part2.D3_PWM
  N3: S1.connector4, Part2.D5_PWM
  N4: S1.connector5, Part2.D6_PWM
  N5: S1.connector6, Part2.D9_PWM
  N6: S1.connector7, M1.pin_2
  N7: S1.connector8, M1.pin_1
  N8: S1.connector9, M2.pin_1
  N9: S1.connector10, M2.pin_2
  N10: Part1.TXD, Part2.D10_PWM/SS
  N11: Part1.RXD, Part2.D11_PWM/MOSI
  VCC: Part1.VCC, Part2.3V3
  N12: VCC1.+, S2.L1

notes:
  18650 Batteries
  3.7V / 2800mAh
  Total Vcc = 7.4V
  9V for Arduino
  HC-05 Bluetooth Module
  L298N DC Motor Driver Board
