# Fritzing sketch id3861_smart_sole_0 (saved by Fritzing 0.9.3b)
breadboards: 1

parts:
  Adafruit_HUZZAH_ESP8266_Breakout1 = Adafruit HUZZAH ESP8266 Breakout [part_number=2471]
  Part1 = InvenSense MPU6050
  R1 = Resistor [tolerance=±5% resistance=15k package="0805 [SMD]"]  # not connected
  R2 = Resistor [tolerance=±5% resistance=15k package="0805 [SMD]"]  # not connected
  R3 = Resistor [tolerance=±5% resistance=15k package="0805 [SMD]"]  # not connected
  J1 = Basic Force Sensing Resistor (FSR) [package=THT]
  J2 = Basic Force Sensing Resistor (FSR) [package=THT]
  J3 = Basic Force Sensing Resistor (FSR) [package=THT]

nets:
  GND: Adafruit_HUZZAH_ESP8266_Breakout1.GND, Part1.GND
  N1: Adafruit_HUZZAH_ESP8266_Breakout1.#13, J1.pin_0
  N2: Adafruit_HUZZAH_ESP8266_Breakout1.#12, J3.pin_0
  N3: Adafruit_HUZZAH_ESP8266_Breakout1.#14, J2.pin_0
  N4: Adafruit_HUZZAH_ESP8266_Breakout1.#5, Part1.SCL
  N5: Adafruit_HUZZAH_ESP8266_Breakout1.#4, Part1.SDA
  N6: Adafruit_HUZZAH_ESP8266_Breakout1.3V, Part1.VCC
