# Fritzing sketch id3862_1relay_compact_v1.0_0 (saved by Fritzing 0.9.3b)
circuit board: 4.9cm x 4.86cm
breadboards: 1

parts:
  U1 = atmega328 [package=dip]
  Part1 = NRF24L01+ Breakout Board  # not connected
  JP1 = Header 4 [package=molex-1x4_lock]
  Q1 = NPN-Transistor [part_number=2N2222A package="TO92 [THT]"]
  R1 = resistor-upright [tolerance=±5% resistance=1k]
  IC1 = Voltage Regulator LM1117 [package=sot223]
  OMRON1 = OMRON PCB Power Relay – G5LE [part_number=JQC-3F(T73) package=THT]
  JP4 = Header 1 [package=1x01_offset]
  Y1 = Resonator [frequency="16 Mhz" package=THT]
  R2 = resistor-upright [tolerance=±5% resistance=1M]
  C3 = Capacitor Polarized [package=cpol-radial-10uf-25v]
  JP6 = header8_1.27mm_pitch_smd [part_number="nRF24L01 SMD"]
  D1 = diode_upright [part_number=1N4001]
  HLK-PM3 = HLK-PM01_correct_holes
  J3 = screw terminal, 3 pins
  J7 = screw terminal, 3 pins
  J5 = screw terminal, 2 pins
  J4 = screw terminal, 4 pins
  J6 = screw terminal, 3 pins
  J8 = screw terminal, 2 pins
  J9 = screw terminal, 3 pins

nets:
  N1: U1.D0_(RX), JP1.4
  N2: U1.D1_(TX), JP1.3
  N3: U1.D2, R1.connector1
  N4: U1.D3_(PWM), J5.pin2
  N5: U1.D4, J5.pin1
  N6: U1.VCC, U1.AVCC, JP1.2, IC1.IN, OMRON1.COIL1, D1.connector1, J3.pin3
  GND: U1.GND, JP1.1, Q1.E, IC1.ADJ, Y1.GND, C3.-, JP6.connector7, HLK-PM3.connector2, J3.pin2
  N7: U1.XLAT1, Y1.0, R2.connector0
  N8: U1.XLAT2, Y1.pin_1, R2.connector1
  N9: U1.D5_(PWM), J4.pin4
  N10: U1.D6_(PWM), J4.pin3
  N11: U1.D7, J4.pin2
  N12: U1.D8, J4.pin1
  N13: U1.D9_(PWM), JP6.connector1
  N14: U1.D10_(PWM), JP6.connector2
  N15: U1.D11_(PWM), JP6.connector4
  N16: U1.D12, JP6.connector5
  N17: U1.D13, JP6.connector3
  N18: U1.A0, J7.pin3
  N19: U1.A1, J7.pin2
  N20: U1.A2, J7.pin1
  N21: U1.A3, J6.pin1
  N22: U1.A4, J6.pin2
  N23: U1.A5, J6.pin3
  N24: Q1.B, R1.connector0
  N25: Q1.C, OMRON1.COIL2, D1.connector0
  N26: IC1.OUT, C3.+, JP6.connector0, J3.pin1
  N27: OMRON1.A, J9.pin1
  N28: OMRON1.C, J9.pin3
  N29: OMRON1.B, J9.pin2
  N30: JP4.1, HLK-PM3.connector3
  N31: HLK-PM3.connector0, J8.pin1
  N32: HLK-PM3.connector1, J8.pin2

notes:
  nRF24l01+ micro with SMD header
  +3.3V
  GND
  +5V
  D8
  D7
  D6
  D3
  D4
  A4
  A3
  A5
  D5
  1relay_compact_v1.0
  180121 by PowerPenguin
  Multi-purpose MySensor Node for wall
  socket/switch integration based on
  ATmega328p and nRF24L01
  Vcc
  RX
  TX
