# Fritzing sketch id3863_SmartVolumeSketch_0 (saved by Fritzing 0.9.3b)
breadboards: 1

parts:
  Part3 = Arduino Uno (Rev3)
  Part2 = Bluetooth HC-05 Macho
  R1 = Resistor [tolerance=±5% resistance=1k package="0805 [SMD]"]
  R3 = Resistor [tolerance=±5% resistance=1k package="0805 [SMD]"]
  KY-038_(big_sound) = Breakout Board for Electret Microphone
  R2 = Resistor [tolerance=±5% resistance=1k package="0805 [SMD]"]

nets:
  N1: Part3.A0, KY-038_(big_sound).AUD
  N2: Part3.D0/RX, Part2.TXD, R3.Pin_0
  N3: Part3.D1/TX, R3.Pin_1
  VCC: Part3.5V, Part2.VCC, KY-038_(big_sound).VCC
  GND: Part3.GND, Part2.GND, KY-038_(big_sound).GND, R2.Pin_1
  N4: Part2.RXD, R1.Pin_1
  N5: R1.Pin_0, R2.Pin_0

notes:
  left to right:
  - AUD (analog input)
  - GND (ground)
  - VCC (power)
  Self I use the HC-04, fritzing only has HC-05 available. Should also work fine!
