# Fritzing sketch id3864_led_dice_attiny85_0 (saved by Fritzing 0.9.3b)
breadboards: 1

parts:
  U1 = attiny85 [package=dip]
  R1 = Resistor [tolerance=±5% resistance=10k package="0805 [SMD]"]
  S1 = Pushbutton [package="[THT]"]
  VCC1 = Battery
  LED1 = smd LED [color="Red (633nm)" package="0805 [SMD]"]
  LED2 = smd LED [color="Red (633nm)" package="0805 [SMD]"]
  LED3 = smd LED [color="Red (633nm)" package="0805 [SMD]"]
  LED4 = smd LED [color="Red (633nm)" package="0805 [SMD]"]
  LED5 = smd LED [color="Red (633nm)" package="0805 [SMD]"]
  LED6 = smd LED [color="Red (633nm)" package="0805 [SMD]"]
  LED7 = smd LED [color="Red (633nm)" package="0805 [SMD]"]

nets:
  N1: U1.Pin_2, R1.Pin_0, S1.Pin_3, S1.Pin_4
  N2: U1.Pin_3, LED1.anode, LED7.anode
  N3: U1.Pin_4, R1.Pin_1, VCC1.-, LED1.cathode, LED2.cathode, LED3.cathode, LED4.cathode, LED5.cathode, LED6.cathode, LED7.cathode
  N4: U1.Pin_5, LED3.anode, LED5.anode
  N5: U1.Pin_6, LED4.anode
  N6: U1.Pin_7, LED2.anode, LED6.anode
  N7: U1.Pin_8, S1.Pin_2, VCC1.+
