# Fritzing sketch id3865_SMD_Relay_Board_0 (saved by Fritzing 0.9.3b)
circuit board: 7.34719cm x 5.23052cm
breadboards: 1

parts:
  OMRON1 = OMRON PCB Power Relay – G5LE [part_number="G5LE-1\n" package=THT]
  OMRON2 = OMRON PCB Power Relay – G5LE [part_number="G5LE-1\n" package=THT]
  OMRON3 = OMRON PCB Power Relay – G5LE [part_number="G5LE-1\n" package=THT]
  OMRON4 = OMRON PCB Power Relay – G5LE [part_number="G5LE-1\n" package=THT]
  D1 = Zener Diode [part_number=1N4732A breakdown_voltage=3.6V package="Melf DO-213 AB [SMD]"]
  D2 = Zener Diode [part_number=1N4732A breakdown_voltage=3.6V package="Melf DO-213 AB [SMD]"]
  D3 = Zener Diode [part_number=1N4732A breakdown_voltage=3.6V package="Melf DO-213 AB [SMD]"]
  D4 = Zener Diode [part_number=1N4732A breakdown_voltage=3.6V package="Melf DO-213 AB [SMD]"]
  Q1 = TRANSISTOR_NPN [package=sot23]
  Q2 = TRANSISTOR_NPN [package=sot23]
  Q3 = TRANSISTOR_NPN [package=sot23]
  Q4 = TRANSISTOR_NPN [package=sot23]
  J1 = screw terminal, 3 pins
  J2 = screw terminal, 3 pins
  J3 = screw terminal, 3 pins
  J4 = screw terminal, 3 pins
  R1 = Resistor [tolerance=±5% resistance=220 package="0805 [SMD]"]
  R2 = Resistor [tolerance=±5% resistance=220 package="0805 [SMD]"]
  R3 = Resistor [tolerance=±5% resistance=220 package="0805 [SMD]"]
  R4 = Resistor [tolerance=±5% resistance=220 package="0805 [SMD]"]
  R5 = Resistor [tolerance=±5% resistance=220 package="0805 [SMD]"]
  R6 = Resistor [tolerance=±5% resistance=220 package="0805 [SMD]"]
  R7 = Resistor [tolerance=±5% resistance=220 package="0805 [SMD]"]
  R8 = Resistor [tolerance=±5% resistance=220 package="0805 [SMD]"]
  U1 = Sharp PC817 [package=THT]
  U2 = Sharp PC817 [package=THT]
  U3 = Sharp PC817 [package=THT]
  U4 = Sharp PC817 [package=THT]
  J5 = male pin header, 6 pins [form="♂ (male)"]
  LED1 = smd LED [color="Red (633nm)" package="1206 [SMD]"]
  LED2 = smd LED [color="Red (633nm)" package="1206 [SMD]"]
  LED3 = smd LED [color="Red (633nm)" package="1206 [SMD]"]
  LED4 = smd LED [color="Red (633nm)" package="1206 [SMD]"]

nets:
  N1: OMRON1.A, J1.pin3
  N2: OMRON1.COIL1, D1.cathode, U1.Pin_4
  N3: OMRON1.C, J1.pin2
  N4: OMRON1.COIL2, OMRON2.COIL2, OMRON3.COIL2, OMRON4.COIL2, D1.anode, D2.anode, D3.anode, D4.anode, Q1.C, Q2.C, Q3.C, Q4.C, J5.pin1
  N5: OMRON1.B, J1.pin1
  N6: OMRON2.A, J2.pin3
  N7: OMRON2.COIL1, D2.cathode, U2.Pin_4
  N8: OMRON2.C, J2.pin2
  N9: OMRON2.B, J2.pin1
  N10: OMRON3.A, J3.pin3
  N11: OMRON3.COIL1, D3.cathode, U3.Pin_4
  N12: OMRON3.C, J3.pin2
  N13: OMRON3.B, J3.pin1
  N14: OMRON4.A, J4.pin3
  N15: OMRON4.COIL1, D4.cathode, U4.Pin_4
  N16: OMRON4.C, J4.pin2
  N17: OMRON4.B, J4.pin1
  N18: Q1.B, R1.Pin_0
  N19: Q1.E, Q2.E, Q3.E, Q4.E, J5.pin6, LED1.anode, LED2.anode, LED3.anode, LED4.anode
  N20: Q2.B, R3.Pin_0
  N21: Q3.B, R5.Pin_0
  N22: Q4.B, R8.Pin_0
  N23: R1.Pin_1, U1.Pin_3
  N24: R2.Pin_0, J5.pin5
  N25: R2.Pin_1, U1.Pin_1
  N26: R3.Pin_1, U2.Pin_3
  N27: R4.Pin_0, J5.pin4
  N28: R4.Pin_1, U2.Pin_1
  N29: R5.Pin_1, U3.Pin_3
  N30: R6.Pin_0, J5.pin3
  N31: R6.Pin_1, U3.Pin_1
  N32: R7.Pin_0, J5.pin2
  N33: R7.Pin_1, U4.Pin_1
  N34: R8.Pin_1, U4.Pin_3
  N35: U1.Pin_2, LED1.cathode
  N36: U2.Pin_2, LED2.cathode
  N37: U3.Pin_2, LED3.cathode
  N38: U4.Pin_2, LED4.cathode
