# Fritzing sketch id3866_pcb_smd_breakboard_0 (saved by Fritzing 0.7.4b)
breadboards: 1

parts:
  IC1 = SO08 [chip_label=IC spacing=300mil package=SO]
  Pad1 = Pad [width=9 height=1.5 connect=south]  # not connected
  Pad2 = Pad [width=7.5 height=1.5 connect=south]  # not connected
  Pad3 = Pad [width=9 height=1.5 connect=south]  # not connected
  Pad4 = Pad [width=3 height=1.5 connect=south]  # not connected
  Pad5 = Pad [width=3 height=1.5 connect=south]  # not connected
  Pad6 = Pad [width=2 height=1.5 connect=center]
  Pad7 = Pad [width=2 height=1.5 connect=center]
  Pad8 = Pad [width=2 height=1.5 connect=center]
  Pad9 = Pad [width=2 height=1.5 connect=center]
  Pad10 = Pad [width=2 height=1.5 connect=west]  # not connected
  Pad11 = Pad [width=2 height=1.5 connect=west]  # not connected
  Pad12 = Pad [width=2 height=1.5 connect=west]  # not connected
  Pad13 = Pad [width=2 height=1.5 connect=west]  # not connected
  Pad14 = Pad [width=2 height=1.5 connect=center]
  Pad15 = Pad [width=2 height=1.5 connect=center]
  Pad16 = Pad [width=2 height=1.5 connect=center]
  Pad17 = Pad [width=2 height=1.5 connect=center]
  Pad18 = Pad [width=2 height=1.5 connect=east]  # not connected
  Pad19 = Pad [width=2 height=1.5 connect=east]  # not connected
  Pad20 = Pad [width=2 height=1.5 connect=east]  # not connected
  Pad21 = Pad [width=2 height=1.5 connect=east]  # not connected
  Pad22 = Pad [width=2 height=4 connect=east]  # not connected
  Pad23 = Pad [width=2 height=4 connect=east]  # not connected
  Pad24 = Pad [width=9 height=1.5 connect=south]  # not connected
  Pad25 = Pad [width=7.5 height=1.5 connect=south]  # not connected
  Pad26 = Pad [width=9 height=1.5 connect=south]  # not connected
  Pad27 = Pad [width=2 height=4 connect=north]
  Pad28 = Pad [width=2 height=4 connect=center]
  Pad29 = Pad [width=3 height=1.5 connect=south]  # not connected
  Pad30 = Pad [width=3 height=1.5 connect=south]  # not connected
  IC2 = SO08 [chip_label=IC spacing=300mil package=SO]
  Pad31 = Pad [width=2 height=4 connect=east]  # not connected
  Pad32 = Pad [width=2 height=4 connect=east]  # not connected
  Pad33 = Pad [width=9 height=1.5 connect=south]  # not connected
  Pad34 = Pad [width=7.5 height=1.5 connect=south]  # not connected
  Pad35 = Pad [width=9 height=1.5 connect=south]  # not connected
  Pad36 = Pad [width=2 height=4 connect=center]
  Pad37 = Pad [width=2 height=4 connect=center]
  Pad38 = Pad [width=2 height=1.5 connect=east]  # not connected
  Pad39 = Pad [width=2 height=1.5 connect=east]  # not connected
  Pad40 = Pad [width=2 height=1.5 connect=east]  # not connected
  Pad41 = Pad [width=2 height=1.5 connect=east]  # not connected
  Pad42 = Pad [width=2 height=1.5 connect=center]
  Pad43 = Pad [width=2 height=1.5 connect=center]
  Pad44 = Pad [width=2 height=1.5 connect=center]
  Pad45 = Pad [width=2 height=1.5 connect=center]
  Pad46 = Pad [width=2 height=1.5 connect=west]  # not connected
  Pad47 = Pad [width=2 height=1.5 connect=west]  # not connected
  Pad48 = Pad [width=2 height=1.5 connect=west]  # not connected
  Pad49 = Pad [width=2 height=1.5 connect=west]  # not connected
  Pad50 = Pad [width=2 height=1.5 connect=center]
  Pad51 = Pad [width=2 height=1.5 connect=center]
  Pad52 = Pad [width=2 height=1.5 connect=center]
  Pad53 = Pad [width=2 height=1.5 connect=center]
  Pad54 = Pad [width=3 height=1.5 connect=south]  # not connected
  Pad55 = Pad [width=3 height=1.5 connect=south]  # not connected
  Pad56 = Pad [width=3 height=1.5 connect=south]  # not connected
  Pad57 = Pad [width=3 height=1.5 connect=south]  # not connected
  Pad58 = Pad [width=9 height=1.5 connect=south]  # not connected
  Pad59 = Pad [width=7.5 height=1.5 connect=center]
  Pad60 = Pad [width=9 height=1.5 connect=center]
  IC3 = SO08 [chip_label=IC spacing=300mil package=SO]
  Pad61 = Pad [width=2 height=4 connect=east]  # not connected
  Pad62 = Pad [width=2 height=4 connect=east]  # not connected
  Pad63 = Pad [width=9 height=1.5 connect=south]  # not connected
  Pad64 = Pad [width=7.5 height=1.5 connect=south]  # not connected
  Pad65 = Pad [width=9 height=1.5 connect=south]  # not connected
  Pad66 = Pad [width=2 height=4 connect=center]
  Pad67 = Pad [width=2 height=4 connect=center]
  Pad68 = Pad [width=2 height=1.5 connect=east]  # not connected
  Pad69 = Pad [width=2 height=1.5 connect=east]  # not connected
  Pad70 = Pad [width=2 height=1.5 connect=east]  # not connected
  Pad71 = Pad [width=2 height=1.5 connect=east]  # not connected
  Pad72 = Pad [width=2 height=1.5 connect=center]
  Pad73 = Pad [width=2 height=1.5 connect=center]
  Pad74 = Pad [width=2 height=1.5 connect=center]
  Pad75 = Pad [width=2 height=1.5 connect=center]
  Pad76 = Pad [width=2 height=1.5 connect=west]  # not connected
  Pad77 = Pad [width=2 height=1.5 connect=west]  # not connected
  Pad78 = Pad [width=2 height=1.5 connect=west]  # not connected
  Pad79 = Pad [width=2 height=1.5 connect=west]  # not connected
  Pad80 = Pad [width=2 height=1.5 connect=center]
  Pad81 = Pad [width=2 height=1.5 connect=center]
  Pad82 = Pad [width=2 height=1.5 connect=center]
  Pad83 = Pad [width=2 height=1.5 connect=center]
  Pad84 = Pad [width=3 height=1.5 connect=south]  # not connected
  Pad85 = Pad [width=3 height=1.5 connect=south]  # not connected
  Pad86 = Pad [width=3 height=1.5 connect=south]  # not connected
  Pad87 = Pad [width=3 height=1.5 connect=south]  # not connected
  Pad88 = Pad [width=9 height=1.5 connect=center]
  Pad89 = Pad [width=7.5 height=1.5 connect=east]
  Pad90 = Pad [width=9 height=1.5 connect=south]  # not connected
  IC4 = SO08 [chip_label=IC spacing=300mil package=SO]
  Pad91 = Pad [width=2 height=4 connect=east]  # not connected
  Pad92 = Pad [width=2 height=4 connect=east]  # not connected
  Pad93 = Pad [width=9 height=1.5 connect=south]  # not connected
  Pad94 = Pad [width=7.5 height=1.5 connect=center]
  Pad95 = Pad [width=9 height=1.5 connect=center]
  Pad96 = Pad [width=2 height=4 connect=east]  # not connected
  Pad97 = Pad [width=2 height=4 connect=east]  # not connected
  Pad98 = Pad [width=2 height=1.5 connect=east]  # not connected
  Pad99 = Pad [width=2 height=1.5 connect=east]  # not connected
  Pad100 = Pad [width=2 height=1.5 connect=east]  # not connected
  Pad101 = Pad [width=2 height=1.5 connect=east]  # not connected
  Pad102 = Pad [width=2 height=1.5 connect=center]
  Pad103 = Pad [width=2 height=1.5 connect=center]
  Pad104 = Pad [width=2 height=1.5 connect=center]
  Pad105 = Pad [width=2 height=1.5 connect=center]
  Pad106 = Pad [width=2 height=1.5 connect=west]  # not connected
  Pad107 = Pad [width=2 height=1.5 connect=west]  # not connected
  Pad108 = Pad [width=2 height=1.5 connect=west]  # not connected
  Pad109 = Pad [width=2 height=1.5 connect=west]  # not connected
  Pad110 = Pad [width=2 height=1.5 connect=center]
  Pad111 = Pad [width=2 height=1.5 connect=center]
  Pad112 = Pad [width=2 height=1.5 connect=center]
  Pad113 = Pad [width=2 height=1.5 connect=center]
  Pad114 = Pad [width=3 height=1.5 connect=south]  # not connected
  Pad115 = Pad [width=3 height=1.5 connect=south]  # not connected
  Pad116 = Pad [width=3 height=1.5 connect=south]  # not connected
  Pad117 = Pad [width=3 height=1.5 connect=south]  # not connected
  Pad118 = Pad [width=9 height=1.5 connect=south]  # not connected
  Pad119 = Pad [width=7.5 height=1.5 connect=south]  # not connected
  Pad120 = Pad [width=9 height=1.5 connect=south]  # not connected

nets:
  N1: IC1.1, Pad6.pad
  N2: IC1.2, Pad7.pad
  N3: IC1.3, Pad8.pad
  N4: IC1.4, Pad9.pad
  N5: IC1.5, Pad16.pad
  N6: IC1.6, Pad14.pad
  N7: IC1.7, Pad15.pad
  N8: IC1.8, Pad17.pad
  N9: Pad27.pad, Pad60.pad
  N10: Pad28.pad, Pad59.pad
  N11: IC2.1, Pad43.pad
  N12: IC2.2, Pad45.pad
  N13: IC2.3, Pad44.pad
  N14: IC2.4, Pad42.pad
  N15: IC2.5, Pad53.pad
  N16: IC2.6, Pad52.pad
  N17: IC2.7, Pad51.pad
  N18: IC2.8, Pad50.pad
  N19: Pad36.pad, Pad88.pad
  N20: Pad37.pad, Pad89.pad
  N21: IC3.1, Pad83.pad
  N22: IC3.2, Pad82.pad
  N23: IC3.3, Pad81.pad
  N24: IC3.4, Pad80.pad
  N25: IC3.5, Pad73.pad
  N26: IC3.6, Pad75.pad
  N27: IC3.7, Pad74.pad
  N28: IC3.8, Pad72.pad
  N29: Pad66.pad, Pad95.pad
  N30: Pad67.pad, Pad94.pad
  N31: IC4.1, Pad103.pad
  N32: IC4.2, Pad105.pad
  N33: IC4.3, Pad104.pad
  N34: IC4.4, Pad102.pad
  N35: IC4.5, Pad113.pad
  N36: IC4.6, Pad112.pad
  N37: IC4.7, Pad111.pad
  N38: IC4.8, Pad110.pad

notes:
  SMD Snap Off
  rd@tilde.se
  Breakout
