# Fritzing sketch id3867_Smiling_snow_ball_0 (saved by Fritzing 0.9.3b)

parts:
  Part1 = MKR1000
  Part2 = LED Matrix - Serial Interface - Red/Green/Blue
  Part4 = LED Matrix - Serial Interface - Red/Green/Blue
  Part6 = LED Matrix - Serial Interface - Red/Green/Blue
  Part7 = LED Matrix - Serial Interface - Red/Green/Blue
  Part8 = LED Matrix - Serial Interface - Red/Green/Blue
  Part9 = LED Matrix - Serial Interface - Red/Green/Blue

nets:
  N1: Part1.connector24, Part7.CS, Part8.CS, Part9.CS
  N2: Part1.connector25, Part2.SCK, Part4.SCK, Part6.SCK
  N3: Part1.connector26, Part2.MOSI
  N4: Part1.connector27, Part2.CS, Part4.CS, Part6.CS
  N5: Part1.connector51, Part7.SCK, Part8.SCK, Part9.SCK
  N6: Part1.connector52, Part7.MOSI
  VCC: Part2.VCC, Part4.VCC, Part6.VCC, Part7.VCC, Part8.VCC, Part9.VCC
  N7: Part2.MISO, Part4.MOSI
  GND: Part2.GND, Part4.GND, Part6.GND, Part7.GND, Part8.GND, Part9.GND
  N8: Part4.MISO, Part6.MOSI
  N9: Part7.MISO, Part9.MOSI
  N10: Part8.MOSI, Part9.MISO

notes:
  D0 = CLK
  D1 = DIN
  D2 = CS
  D3 = CLK
  D4 = DIN
  D5 = CS
