# Fritzing sketch id3868_smoke_sensor_0 (saved by Fritzing 0.9.2b)
breadboards: 1

parts:
  Part1 = Arduino Uno (Rev3)
  R1 = Resistor [tolerance=±5% resistance=100 package=THT]  # not connected
  LED1 = LED - 5mm [color="Red (633nm)" package="5 mm [THT]"]
  J1 = Piezo Speaker
  R2 = Resistor [tolerance=±5% resistance=100 package=THT]  # not connected
  S1 = Pushbutton [package="[THT]"]
  R3 = Resistor [tolerance=±5% resistance=10k package=THT]
  U1 = GAS_SENSOR [package=mq-3]

nets:
  N1: Part1.A0, U1.H2
  N2: Part1.D9_PWM, J1.pin2
  N3: Part1.D13/SCK, LED1.anode
  N4: Part1.D4, R3.Pin_0
  N5: Part1.5V, U1.B1
  GND: S1.Pin_2
  N6: S1.Pin_3, S1.Pin_4, R3.Pin_1
