# Fritzing sketch id3869_FritzingSketch_0 (saved by Fritzing 0.9.3b)
breadboards: 1
perfboards: 2

parts:
  Part1 = Arduino Uno (Rev3)
  LCD1 = LCD screen  # not connected
  Q1 = Basic FET P-Channel [package="TO220 [THT]"]
  R1 = Resistor [tolerance=±5% resistance=220 package=THT]
  RE1 = Rotary Encoder [package=THT]
  S1 = Pushbutton [package=THT]
  Power_plug1 = Power plug
  Power_plug2 = Power plug
  J1 = Basic Servo
  M1 = DC Motor
  J5 = Screw terminal - 2 pins [package=THT]  # not connected
  J7 = male pin header, 4 pins [form="♂ (male)"]
  J8 = male pin header, 4 pins [form="♂ (male)"]
  J6 = male pin header, 5 pins [form="♂ (male)"]
  J2 = male pin header, 5 pins [form="♂ (male)"]

nets:
  N1: Part1.A0, J6.pin3, J2.pin3
  N2: Part1.A1, J6.pin4, J2.pin4
  N3: Part1.A2, J6.pin5, J2.pin5
  N4: Part1.A4/SDA, J7.pin3, J8.pin3
  N5: Part1.A5/SCL, J7.pin4, J8.pin4
  N6: Part1.D9_PWM, J1.pulse
  N7: Part1.D11_PWM/MOSI, R1.Pin_1, S1.leg1
  N8: Part1.D2, RE1.EncoderPinB
  N9: Part1.D3_PWM, RE1.EncoderPinA
  N10: Part1.D5_PWM, Q1.gate
  VCC: Part1.5V, S1.leg0, Power_plug2.VCC, J1.vcc, J7.pin2, J8.pin2
  GND: Part1.GND, Q1.source, R1.Pin_0, RE1.EncoderPinC, Power_plug2.GND, J1.gnd, J7.pin1, J8.pin1, J6.pin1, J6.pin2, J2.pin1, J2.pin2
  N11: Q1.drain, M1.pin_2
  N12: Power_plug1.VCC, M1.pin_1

notes:
  I2C LCD Connector
  Temp Sensor
  5v DC
  12v DC
  DC Fan
  Air Inlet Controller
