# Fritzing sketch id386_Untitled_Sketch_0 (saved by Fritzing 0.9.0b)
breadboards: 1

parts:
  S1 = Toggle Switch [package=THT]
  S2 = Pushbutton [package="[THT]"]
  7_Segment1 = 7 Segment Display
  7_Segment2 = 7 Segment Display
  Part1 = Arduino Leonardo (Rev3b)
  R1 = Resistor [tolerance=±5% resistance=220 package=THT]  # not connected
  R2 = Resistor [tolerance=±5% resistance=220 package=THT]
  R3 = Resistor [tolerance=±5% resistance=220 package=THT]
  R4 = Resistor [tolerance=±5% resistance=220 package=THT]

nets:
  N1: S1.COM, Part1.D8/A8
  N2: S1.L2, S2.Pin_3, S2.Pin_4, Part1.GND, R2.Pin_1, R3.Pin_1, R4.Pin_0
  N3: S2.Pin_1, S2.Pin_2, Part1.D12/A11
  N4: 7_Segment1.Segment_E, Part1.D5_PWM
  N5: 7_Segment1.Segment_D, Part1.D6_PWM/A7
  N6: 7_Segment1.common_anode, R2.Pin_0, R4.Pin_1
  N7: 7_Segment1.Segment_C, Part1.D7
  N8: 7_Segment1.Segment_B, Part1.A1
  N9: 7_Segment1.Segment_A, Part1.D2/SDA
  N10: 7_Segment1.Segment_F, Part1.D3_PWM/SCL
  N11: 7_Segment1.Segment_G, Part1.D4/A6
  N12: 7_Segment2.Segment_E, Part1.D9_PWM/A9
  N13: 7_Segment2.Segment_D, Part1.D10_PWM/A10
  N14: 7_Segment2.common_anode, R3.Pin_0
  N15: 7_Segment2.Segment_C, Part1.D11_PWM
  N16: 7_Segment2.Segment_B, Part1.A5
  N17: 7_Segment2.Segment_A, Part1.A4
  N18: 7_Segment2.Segment_F, Part1.A3
  N19: 7_Segment2.Segment_G, Part1.A2
