# Fritzing sketch id3870_sms_bouton_0 (saved by Fritzing 0.9.2b)
breadboards: 1

parts:
  S1 = Pushbutton [package="[THT]"]
  LED1 = LED - 5mm [color="Red (633nm)" package="5 mm [THT]"]
  R1 = Resistor [tolerance=±5% resistance=220 package=THT]
  R2 = Resistor [tolerance=±5% resistance=10k package=THT]
  1Sheeld1 = 1Sheeld
  Composant1 = Arduino Uno (Rev3)  # not connected
  Smart_Phone1 = Smart Phone  # not connected

nets:
  N1: S1.Pin_1, S1.Pin_2, R2.Pin_1, 1Sheeld1.connector9
  N2: S1.Pin_3, S1.Pin_4, 1Sheeld1.connector28
  N3: LED1.cathode, R1.Pin_1
  N4: LED1.anode, 1Sheeld1.connector10
  N5: R1.Pin_0, R2.Pin_0, 1Sheeld1.connector27
