# Fritzing sketch id3872_SN74HC595N_0 (saved by Fritzing 0.9.3b)
breadboards: 2

parts:
  U4 = 74HC595 [package="DIP16 [THT]"]
  J1 = STM32 Nucleo boards
  R2 = Resistor [tolerance=±5% resistance=220 package=THT]
  R3 = Resistor [tolerance=±5% resistance=220 package=THT]
  R4 = Resistor [tolerance=±5% resistance=220 package=THT]
  R5 = Resistor [tolerance=±5% resistance=220 package=THT]
  R6 = Resistor [tolerance=±5% resistance=220 package=THT]
  R7 = Resistor [tolerance=±5% resistance=220 package=THT]
  R8 = Resistor [tolerance=±5% resistance=220 package=THT]
  R9 = Resistor [tolerance=±5% resistance=220 package=THT]
  R10 = Resistor [tolerance=±5% resistance=220 package=THT]
  R11 = Resistor [tolerance=±5% resistance=220 package=THT]
  R12 = Resistor [tolerance=±5% resistance=220 package=THT]
  R13 = Resistor [tolerance=±5% resistance=220 package=THT]
  R14 = Resistor [tolerance=±5% resistance=220 package=THT]
  R15 = Resistor [tolerance=±5% resistance=220 package=THT]
  R16 = Resistor [tolerance=±5% resistance=220 package=THT]
  R17 = Resistor [tolerance=±5% resistance=220 package=THT]
  U5 = 74HC595 [package="DIP16 [THT]"]
  LED1 = LED - 5mm [color="Red (633nm)" package="5 mm [THT]"]
  LED2 = LED - 5mm [color="Red (633nm)" package="5 mm [THT]"]
  LED3 = LED - 5mm [color="Red (633nm)" package="5 mm [THT]"]
  LED4 = LED - 5mm [color="Red (633nm)" package="5 mm [THT]"]
  LED5 = LED - 5mm [color="Red (633nm)" package="5 mm [THT]"]
  LED6 = LED - 5mm [color="Red (633nm)" package="5 mm [THT]"]
  LED7 = LED - 5mm [color="Red (633nm)" package="5 mm [THT]"]
  LED8 = LED - 5mm [color="Red (633nm)" package="5 mm [THT]"]
  LED9 = LED - 5mm [color="Blue (430nm)" package="5 mm [THT]"]
  LED10 = LED - 5mm [color="Blue (430nm)" package="5 mm [THT]"]
  LED11 = LED - 5mm [color="Blue (430nm)" package="5 mm [THT]"]
  LED12 = LED - 5mm [color="Blue (430nm)" package="5 mm [THT]"]
  LED13 = LED - 5mm [color="Blue (430nm)" package="5 mm [THT]"]
  LED14 = LED - 5mm [color="Blue (430nm)" package="5 mm [THT]"]
  LED15 = LED - 5mm [color="Blue (430nm)" package="5 mm [THT]"]
  LED16 = LED - 5mm [color="Blue (430nm)" package="5 mm [THT]"]
  C1 = Electrolytic Capacitor [capacitance=1µF package="100 mil [THT, electrolytic]"]

nets:
  N1: U4.Q1, R3.Pin_1
  N2: U4.Q2, R4.Pin_1
  N3: U4.Q3, R5.Pin_1
  N4: U4.Q4, R6.Pin_1
  N5: U4.Q5, R7.Pin_1
  N6: U4.Q6, R8.Pin_1
  N7: U4.Q7, R9.Pin_1
  GND: U4.GND, U4.OE, J1.GND, U5.GND, U5.OE, C1.-
  N8: U4.Q7', U5.DS
  VCC: U4.MR, U4.VCC, J1.5V, U5.MR, U5.VCC
  N9: U4.SH_CP, J1.D8, U5.SH_CP
  N10: U4.ST_CP, J1.D9_PWM, U5.ST_CP, C1.+
  N11: U4.DS, J1.D10_PWM/SS
  N12: U4.Q0, R2.Pin_1
  N13: R2.Pin_0, LED1.anode
  N14: R3.Pin_0, LED2.anode
  N15: R4.Pin_0, LED3.anode
  N16: R5.Pin_0, LED4.anode
  N17: R6.Pin_0, LED5.anode
  N18: R7.Pin_0, LED6.anode
  N19: R8.Pin_0, LED7.anode
  N20: R9.Pin_0, LED8.anode
  N21: R10.Pin_0, LED9.anode
  N22: R10.Pin_1, U5.Q0
  N23: R11.Pin_0, LED10.anode
  N24: R11.Pin_1, U5.Q1
  N25: R12.Pin_0, LED11.anode
  N26: R12.Pin_1, U5.Q2
  N27: R13.Pin_0, LED12.anode
  N28: R13.Pin_1, U5.Q3
  N29: R14.Pin_0, LED13.anode
  N30: R14.Pin_1, U5.Q4
  N31: R15.Pin_0, LED14.anode
  N32: R15.Pin_1, U5.Q5
  N33: R16.Pin_0, LED15.anode
  N34: R16.Pin_1, U5.Q6
  N35: R17.Pin_0, LED16.anode
  N36: R17.Pin_1, U5.Q7
  N37: LED1.cathode, LED2.cathode, LED3.cathode, LED4.cathode, LED5.cathode, LED6.cathode, LED7.cathode, LED8.cathode, LED9.cathode, LED10.cathode, LED11.cathode, LED12.cathode, LED13.cathode, LED14.cathode, LED15.cathode, LED16.cathode
