# Fritzing sketch id3875_snow_0 (saved by Fritzing 0.9.3b)
breadboards: 1

parts:
  U1 = attiny85 [package=dip]
  C1 = Electrolytic Capacitor [capacitance=10µF package="1010 [SMD, electrolytic]"]
  ANT1 = Antenna
  hc-sr2 = hc-sr04 (fixed)
  BAT1 = Battery Holders [package=battery-aa-kit]
  hc-sr3 = Sigfox

nets:
  N1: U1.Pin_2, hc-sr3.connector1
  N2: U1.Pin_3, hc-sr3.connector2
  N3: U1.Pin_4, C1.-, hc-sr2.connector4, BAT1.-, hc-sr3.connector3
  N4: U1.Pin_5, C1.+, hc-sr2.connector1
  N5: U1.Pin_6, hc-sr2.connector3
  N6: U1.Pin_7, hc-sr2.connector2
  N7: U1.Pin_8, BAT1.+, hc-sr3.connector4
  N8: ANT1.antenna_lead, hc-sr3.connector5
