# Fritzing sketch id3876_s.e._by_teeQ_0 (saved by Fritzing 0.7.12b)
breadboards: 1

parts:
  Q1 = NPN-Transistor [package="TO92 [THT]"]
  VCC1 = Battery
  IC1 = PICAXE-08M [package=THT]
  J1 = Generic female header - 3 pins [package=THT]
  J2 = Generic female header [package=THT]
  J3 = Screw terminal - 2 pins [package=THT]
  J4 = female pin header, 2 pins [form="♀ (female)"]
  J5 = female pin header, 1 pin [form="♀ (female)"]

nets:
  N1: Q1.E, J4.pin2
  N2: Q1.B, IC1.In/Out_1_/_ADC_1
  N3: Q1.C, J3.pin1
  N4: VCC1.-, IC1.0V, J1.pin3
  N5: VCC1.+, IC1.+V
  N6: IC1.Serial_In, J1.pin2
  N7: IC1.In/Out_4_/_ADC_4, J5.pin1
  N8: IC1.In_3_/_Infrain, J2.pin1
  N9: IC1.Serial_Out_/_Out_0_/_Infraout, J1.pin1
  N10: J3.pin2, J4.pin1

notes:
  soda expulsor shieild ver. 1.3
  teeQ
