# Fritzing sketch id3877_sof_servo_0 (saved by Fritzing 0.9.2b)
breadboards: 1

parts:
  Part1 = Arduino Uno (Rev3)
  R1 = Rotary Potentiometer (Small) [maximum_resistance=100kΩ package=THT]
  C1 = Electrolytic Capacitor [capacitance=100µF package="100 mil [THT, electrolytic]"]
  J1 = Basic Servo
  C2 = Electrolytic Capacitor [capacitance=100µF package="100 mil [THT, electrolytic]"]

nets:
  N1: Part1.A0, R1.wiper
  N2: Part1.D9_PWM, J1.pulse
  5V: Part1.5V, R1.leg2, C1.+, J1.vcc, C2.+
  GND: Part1.GND, R1.leg1, C1.-, J1.gnd, C2.-
