# Fritzing sketch id3878_softswitch_0 (saved by Fritzing 0.9.3b)
circuit board: 2.35473cm x 2.84993cm
breadboards: 1

parts:
  Q1 = Basic FET P-Channel [part_number=STP12PF06 package="TO220 [THT]"]
  D1 = Rectifier Diode [part_number=1N4001 package="300 mil [THT]"]
  D2 = Rectifier Diode [part_number=1N4001 package="300 mil [THT]"]
  Q2 = NPN-Transistor [part_number=2N3904 package="TO92 [THT]"]
  R1 = Resistor [tolerance=±5% resistance=100k package=THT]
  R2 = Resistor [tolerance=±5% resistance=100k package=THT]
  R3 = Resistor [tolerance=±5% resistance=100k package=THT]
  S1 = Pushbutton [package="[THT]"]
  A0 = female pin header, 1 pin [form="♀ (female)"]
  D0 = female pin header, 1 pin [form="♀ (female)"]
  5v = female pin header, 2 pins [form="♀ (female)"]
  + = female pin header, 1 pin [form="♀ (female)"]
  - = female pin header, 1 pin [form="♀ (female)"]

nets:
  N1: Q1.gate, D1.anode, Q2.C, R2.Pin_1
  N2: Q1.drain, R1.Pin_0, R2.Pin_0, 5v.pin2
  N3: Q1.source, +.pin1
  N4: D1.cathode, D2.cathode, S1.Pin_3, S1.Pin_4
  N5: D2.anode, R1.Pin_1, D0.pin1
  N6: Q2.E, S1.Pin_1, S1.Pin_2, 5v.pin1, -.pin1
  N7: Q2.B, R3.Pin_1
  N8: R3.Pin_0, A0.pin1

notes:
  +
  -
