# Fritzing sketch id3879_Quadrada (saved by Fritzing 0.8.5b)
breadboards: 1

parts:
  R1 = Resistor [tolerance=±5% resistance=1k package=THT]
  Q1 = NPN-Transistor [package="TO92 [THT]"]
  C1 = Ceramic Capacitor [capacitance=100nF package="100 mil [THT, multilayer]"]
  C2 = Ceramic Capacitor [capacitance=100nF package="100 mil [THT, multilayer]"]
  Q2 = NPN-Transistor [package="TO92 [THT]"]
  R3 = Resistor [tolerance=±5% resistance=1M package=THT]
  Q3 = NPN-Transistor [package="TO92 [THT]"]
  R4 = Resistor [tolerance=±5% resistance=1k package=THT]
  R5 = Resistor [tolerance=±5% resistance=27k package=THT]
  R6 = Resistor [tolerance=±5% resistance=1M package=THT]

nets:
  N1: R1.Pin_0, R3.Pin_1, R4.Pin_0, R5.Pin_0, R6.Pin_0
  N2: R1.Pin_1, Q1.E, C1.0
  N3: Q1.B, C2.0, R6.Pin_1
  N4: C1.1, Q2.B, R3.Pin_0
  N5: C2.1, Q2.E, R4.Pin_1
  N6: Q2.C, Q3.B
  N7: Q3.E, R5.Pin_1
