# Fritzing sketch id3879_Soil_Humidity_Sensor_0 (saved by Fritzing 0.9.2b)
breadboards: 1

parts:
  부품1 = Arduino Uno (Rev3)
  부품2 = Humidity Sensor - HIH-4030 Breakout
  R1 = Resistor [tolerance=±5% resistance=220 package=THT]
  R2 = Resistor [tolerance=±5% resistance=220 package=THT]
  LED1 = LED - 5mm [color="Red (633nm)" package="5 mm [THT]"]
  LED2 = LED - 5mm [color="Green (555nm)" package="5 mm [THT]"]

nets:
  N1: 부품1.A0, 부품2.OUT
  N2: 부품1.D3_PWM, LED1.anode
  N3: 부품1.D4, LED2.anode
  5V: 부품1.5V, 부품2.VCC
  GND: 부품1.GND, 부품2.GND, R1.Pin_1, R2.Pin_1
  N4: R1.Pin_0, LED1.cathode
  N5: R2.Pin_0, LED2.cathode

notes:
  LCD SDA
  LCD SCL
  LCD VCC
  LCD GND
