# Fritzing sketch id3882_Test_moisture_sensor_0 (saved by Fritzing 0.9.3b)

parts:
  Componente1 = Arduino Uno (Rev3)
  KY-019_5V_relay_module = keyes
  J1 = female pin header, 3 pins [form="♀ (female)"]

nets:
  N1: Componente1.A0, J1.pin1
  N2: Componente1.GND, KY-019_5V_relay_module.connector2, J1.pin3
  N3: Componente1.D2, KY-019_5V_relay_module.connector0
  N4: Componente1.D3_PWM, J1.pin2
  N5: Componente1.5V, KY-019_5V_relay_module.connector1

notes:
  Soil moisture sensor test by www.adrirobot.it
  http://www.adrirobot.it/sensori/moisture_sensor/moisture_sensor.htm
  Soil moisture sensor
