# Fritzing sketch id3883_LCD_RTC (saved by Fritzing 0.6.3b)
breadboards: 1

parts:
  LCD1 = LCD screen
  J1 = female pin header, 4 pins [form="♀ (female)"]
  Arduino1 = Arduino
  R1 = Rotary Potentiometer (Small) [maximum_resistance=100kΩ]

nets:
  VSS: LCD1.VSS, LCD1.LED-, J1.pin1, Arduino1.GND, R1.leg2
  VDD: LCD1.VDD, J1.pin2, Arduino1.+5V, R1.leg1
  N1: LCD1.V0, R1.wiper
  N2: LCD1.RS, Arduino1.D12
  N3: LCD1.R/W, Arduino1.D11
  N4: LCD1.E, Arduino1.D10
  N5: LCD1.DB4, Arduino1.D5
  N6: LCD1.DB5, Arduino1.D4
  N7: LCD1.DB6, Arduino1.D3
  N8: LCD1.DB7, Arduino1.D2
  N9: LCD1.LED+, Arduino1.D13
  N10: J1.pin3, Arduino1.A4
  N11: J1.pin4, Arduino1.A5

notes:
  RTC DS1307
  Gnd - Vcc - Sda - Scl
  Pote de 1KOhm
  LCD Display - disposición de pines
  1 2 3 4 5 6 7 8 9 10 11 12 13 14 15 16
  (VSS-VDD-V0-RS-RW-E-D0-D1-D2-D3-D4-D5-D6-D7- A - K )
