# Fritzing sketch id3883_sojusLED_0 (saved by Fritzing 0.7.4b)
breadboards: 5

parts:
  U1 = 74HC595 [package="DIP16 [THT]"]
  led_6 = Screw terminal - 2 pins [package=THT]
  led_7 = Screw terminal - 2 pins [package=THT]
  led_8 = Screw terminal - 2 pins [package=THT]
  led_5 = Screw terminal - 2 pins [package=THT]
  led_3 = Screw terminal - 2 pins [package=THT]
  led_4 = Screw terminal - 2 pins [package=THT]
  led_2 = Screw terminal - 2 pins [package=THT]
  led_1 = Screw terminal - 2 pins [package=THT]
  Arduino = Screw terminal - 2 pins [package=THT]
  SH_CP/ST_CP1 = Screw terminal - 2 pins [package=THT]
  Q7'_/_DS1 = Screw terminal - 2 pins [package=THT]
  Netzteil = Screw terminal - 2 pins [package=THT]
  Q7 = NPN-Transistor [package="TO92 [THT]"]
  Q5 = NPN-Transistor [package="TO92 [THT]"]
  Q6 = NPN-Transistor [package="TO92 [THT]"]
  Q4 = NPN-Transistor [package="TO92 [THT]"]
  Q3 = NPN-Transistor [package="TO92 [THT]"]
  Q2 = NPN-Transistor [package="TO92 [THT]"]
  Q1 = NPN-Transistor [package="TO92 [THT]"]
  Q0 = NPN-Transistor [package="TO92 [THT]"]
  R7 = Resistor [tolerance=±5% resistance=10k package=THT]
  R6 = Resistor [tolerance=±5% resistance=10k package=THT]
  R5 = Resistor [tolerance=±5% resistance=10k package=THT]
  R4 = Resistor [tolerance=±5% resistance=10k package=THT]
  R3 = Resistor [tolerance=±5% resistance=10k package=THT]
  R2 = Resistor [tolerance=±5% resistance=10k package=THT]
  R1 = Resistor [tolerance=±5% resistance=10k package=THT]
  R0 = Resistor [tolerance=±5% resistance=10k package=THT]
  C1 = Electrolytic Capacitor [capacitance=1µF package="100 mil [THT, electrolytic]"]

nets:
  N1: U1.Q1, Q1.B
  N2: U1.Q2, Q2.B
  N3: U1.Q3, Q3.B
  N4: U1.Q4, Q4.B
  N5: U1.Q5, Q5.B
  N6: U1.Q6, Q6.B
  N7: U1.Q7, Q7.B
  N8: U1.GND, U1.OE, Arduino.pin2, Netzteil.pin2, Q7.E, Q5.E, Q6.E, Q4.E, Q3.E, Q2.E, Q1.E, Q0.E, R7.Pin_0, R6.Pin_0, R5.Pin_0, R4.Pin_0, R3.Pin_0, R2.Pin_0, R1.Pin_0, R0.Pin_0, C1.-
  N9: U1.Q7', Q7'_/_DS1.pin2
  N10: U1.MR, U1.VCC, Arduino.pin1, R7.Pin_1, R6.Pin_1, R5.Pin_1, R4.Pin_1, R3.Pin_1, R2.Pin_1, R1.Pin_1, R0.Pin_1
  N11: U1.SH_CP, SH_CP/ST_CP1.pin1
  N12: U1.ST_CP, SH_CP/ST_CP1.pin2, C1.+
  N13: U1.DS, Q7'_/_DS1.pin1
  N14: U1.Q0, Q0.B
  N15: led_6.pin1, led_7.pin1, led_8.pin1, led_5.pin1, led_3.pin1, led_4.pin1, led_2.pin1, led_1.pin1, Netzteil.pin1
  N16: led_6.pin2, Q5.C
  N17: led_7.pin2, Q6.C
  N18: led_8.pin2, Q7.C
  N19: led_5.pin2, Q4.C
  N20: led_3.pin2, Q2.C
  N21: led_4.pin2, Q3.C
  N22: led_2.pin2, Q1.C
  N23: led_1.pin2, Q0.C

notes:
  12V - Netzteil
  led 1 2 3 4 5 6 7 8 | +/-
  +
  -
  12 V
  Slave
  Data
  gnd
  5V
  A1
  A2
  L8
  L7
  L6
  L5
  L4
  L2
  L3
  L1
  LED-Treiber
