# Fritzing sketch id3884_Solar_Charge_Controller_0 (saved by Fritzing 0.9.3b)
perfboards: 1

parts:
  555 = IC, DIP package, 8 pins [chip_label=IC]
  LED1 = LED - 5mm [color="Red (633nm)" package="5 mm [THT]"]
  R1 = Resistor [tolerance=±5% resistance=1k package=THT]
  U1_10K = POT [package=3362u]
  LED2 = LED - 5mm [color="Green (570nm)" package="5 mm [THT]"]
  R2 = Resistor [tolerance=±5% resistance=1k package=THT]
  Q1 = NPN-Transistor [part_number=2N2222 package="TO92 [THT]"]
  R3 = Resistor [tolerance=±5% resistance=1k package=THT]
  R4 = Resistor [tolerance=±5% resistance=330 package=THT]
  R6 = Resistor [tolerance=±5% resistance=100 package=THT]
  Q2 = Basic FET N-Channel [part_number=PowerMOS package="TO220 [THT]"]
  D1 = Rectifier Diode [part_number=1N4007 package="300 mil [THT]"]
  U1 = Voltage Regulator - 5V [package="TO220 [THT]"]
  RELAY1 = CAR RELAY [part_number=NVF4-2 package=THT]
  C1 = Ceramic Capacitor [capacitance=1µF voltage=10V package="100 mil [THT, multilayer]"]
  C2 = Ceramic Capacitor [capacitance=1µF voltage=10V package="100 mil [THT, multilayer]"]
  S1 = Round Pushbutton
  U1_10K1 = POT [package=3362u]
  R7 = Resistor [tolerance=±5% resistance=330 package=THT]
  S2 = Round Pushbutton
  J1 = Screw terminal - 2 pins [package=THT]
  J2 = Screw terminal - 2 pins [package=THT]

nets:
  N1: 555.pin1, S2.leg1
  N2: 555.pin2, U1_10K1.S, S2.leg0
  N3: 555.pin3, LED2.anode, R3.Pin_1
  N4: 555.pin4, 555.pin8, LED1.anode, R4.Pin_0
  N5: 555.pin6, U1_10K.S, S1.leg0
  N6: 555.pin7, R1.Pin_0
  N7: LED1.cathode, R1.Pin_1
  N8: U1_10K.E, U1_10K1.E, R7.Pin_1
  N9: U1_10K.A, R2.Pin_1, Q1.C, Q2.source, U1.GND, C1.0, C2.0, U1_10K1.A, J1.pin1
  N10: LED2.cathode, R2.Pin_0
  N11: Q1.E, R4.Pin_1, R6.Pin_1
  N12: Q1.B, R3.Pin_0
  N13: R6.Pin_0, Q2.gate
  N14: Q2.drain, D1.anode, RELAY1.86
  N15: D1.cathode, U1.output_voltage, RELAY1.85, C2.1, S1.leg1
  N16: U1.input_voltage, RELAY1.87A, C1.1, R7.Pin_0, J2.pin2
  N17: RELAY1.30, J1.pin2
  N18: RELAY1.87, J2.pin1

notes:
  GND
  +VE In
  DUMP
  BAT +VE
