# Fritzing sketch id3885_motion_lighting_0 (saved by Fritzing 0.9.3b)
perfboards: 1

parts:
  solar_cell = SOLAR-IXYS [package=solarbit-12x1]
  solar_cell_2 = SOLAR-IXYS [package=solarbit-12x1]
  solar_cell_3 = SOLAR-IXYS [package=solarbit-12x1]
  solar_cell_4 = SOLAR-IXYS [package=solarbit-12x1]
  solar_cell_5 = SOLAR-IXYS [package=solarbit-12x1]
  Part1 = Power Cell LiPo Charger/Booster
  TP4056_Charger_w/booster = Power Cell LiPo Charger/Booster
  4X_li-ion_batteries = LIPO-2000mAh [package=lipo-2000]
  TP4056_Charger_w/booster_2 = Power Cell LiPo Charger/Booster
  U2 = 555 Timer [package="SO8 [SMD]"]
  C1 = Ceramic Capacitor [capacitance=100nF package="100 mil [THT, multilayer]"]
  C2 = Electrolytic Capacitor [capacitance=1000µF package="300 mil [THT, electrolytic]"]
  Q1 = TRANSISTOR_NPN [package=to-92-ammo]
  R2 = Resistor [tolerance=±5% resistance=1k package="1206 [SMD]"]
  U3 = MLX90614 [package=to-39]
  Q2 = Basic FET N-Channel [package="DPak [SMD]"]
  R4 = Resistor [tolerance=±5% resistance=1k package="1206 [SMD]"]
  R5 = Resistor [tolerance=±5% resistance=10k package="1206 [SMD]"]
  LED1 = LEDs [package=led10mm]
  U1 = SWITCH_SPDT [package=kps-1290]
  R3 = Resistor [tolerance=±5% resistance=10k package="1206 [SMD]"]
  U4 = POT [package=alps_pot]  # not connected

nets:
  N1: solar_cell.A, solar_cell_2.C
  N2: solar_cell.C, Part1.5VIN, TP4056_Charger_w/booster.5VIN
  N3: solar_cell_2.A, solar_cell_3.C
  N4: solar_cell_3.A, solar_cell_4.C
  N5: solar_cell_4.A, solar_cell_5.C
  GND: solar_cell_5.A, Part1.GND, TP4056_Charger_w/booster.GND, 4X_li-ion_batteries.+
  VCC: Part1.VCC, TP4056_Charger_w/booster.VCC, 4X_li-ion_batteries.-
  N6: TP4056_Charger_w/booster.PS, TP4056_Charger_w/booster_2.EN
  N7: TP4056_Charger_w/booster_2.PS, U1.O
  N8: U2.Pin_2, Q1.C, R3.Pin_0
  N9: U2.Pin_3, R4.Pin_0
  N10: U2.Pin_5, C1.0
  N11: U2.Pin_6, U2.Pin_7, C2.+
  N12: Q1.B, R2.Pin_0
  N13: R2.Pin_1, U3.VDD
  N14: Q2.Gate, R4.Pin_1, R5.Pin_0
  N15: Q2.drain, LED1.C
  N16: Q2.source, R5.Pin_1
