# Fritzing sketch id3886_UniversalSolabile_0 (saved by Fritzing 0.7.10b)
breadboards: 1

parts:
  Q1 = Basic_FET_P_Channel [part_number="Digikey FDN327NCT-ND"]
  Q2 = Basic_FET_P_Channel [part_number="Digikey FDN327NCT-ND"]  # not connected
  Pad1 = Pad [width=1 height=1 connect=center]
  Pad2 = Pad [width=1 height=1 connect=center]
  C1 = Ceramic Capacitor [capacitance=100nF package="0805 [SMD, multilayer]"]
  Pad3 = Pad [width=1 height=5 connect=center]  # not connected

nets:
  N1: Q1.connector0, Pad1.pad
  N2: Q1.connector1, Pad2.pad, C1.0
