# Fritzing sketch id3887_solarmotor_0 (saved by Fritzing 0.8.5b)
breadboards: 1

parts:
  Part1 = Arduino Pro Mini v13
  VCC1 = Battery block 9V
  R1 = Resistor [tolerance=±5% resistance=4.7k package=THT]

nets:
  N1: Part1.RAW, VCC1.+
  N2: Part1.GND, VCC1.-, R1.Pin_0
  N3: Part1.A0, R1.Pin_1

notes:
  Solar Panel/battery Connects here
  Output to L298 Dual H Bridge
