# Fritzing sketch id3888_SolarBattery_0 (saved by Fritzing 0.8.5b)

parts:
  Panel-Hook_up_through_voltage_regulator = DC Power [voltage=14]
  Battery = DC Power [voltage=12V]
  Float_Switch/Charger = Voltage Regulator - Variable [package="TO220 [THT]"]

nets:
  N1: Panel-Hook_up_through_voltage_regulator.V+, Float_Switch/Charger.IN
  GND: Panel-Hook_up_through_voltage_regulator.V-
  N2: Battery.V+, Float_Switch/Charger.OUT

notes:
  Connect devices in parralel to the system
