# Fritzing sketch id3889_personalschematic_0 (saved by Fritzing 0.9.3b)

parts:
  Part1 = Power Cell LiPo Charger/Booster
  Part2 = PowerBoost 500 Charger
  D1 = SOLAR-IXYS [package=solarbit-12x1]
  U1 = LIPO-2000mAh [package=lipo-2000]

nets (from the breadboard view):
  N1: Part1.VCC, D1.A
  N2: Part1.GND, Part2.GND_BAT_IN, D1.C, U1.-
  N3: Part1.5VIN, Part2.VBAT_OUT
  N4: Part1.VBATT, U1.+
