# Fritzing sketch id388_binary_counter_0 (saved by Fritzing 0.9.0b)
breadboards: 1

parts:
  S1 = Pushbutton [package="[THT]"]
  R1 = Resistor [tolerance=±5% resistance=220 package=THT]
  LED1 = LED - 5mm [color="Red (633nm)" package="5 mm [THT]"]
  Part1 = Arduino Uno (Rev3)
  LED2 = LED - 5mm [color="Red (633nm)" package="5 mm [THT]"]
  LED3 = LED - 5mm [color="Red (633nm)" package="5 mm [THT]"]
  LED4 = LED - 5mm [color="Red (633nm)" package="5 mm [THT]"]
  LED5 = LED - 5mm [color="Red (633nm)" package="5 mm [THT]"]
  LED6 = LED - 5mm [color="Red (633nm)" package="5 mm [THT]"]
  LED7 = LED - 5mm [color="Red (633nm)" package="5 mm [THT]"]
  LED8 = LED - 5mm [color="Red (633nm)" package="5 mm [THT]"]
  R2 = Resistor [tolerance=±5% resistance=220 package=THT]
  R3 = Resistor [tolerance=±5% resistance=220 package=THT]
  R4 = Resistor [tolerance=±5% resistance=220 package=THT]
  R5 = Resistor [tolerance=±5% resistance=220 package=THT]
  R6 = Resistor [tolerance=±5% resistance=220 package=THT]
  R7 = Resistor [tolerance=±5% resistance=220 package=THT]
  R8 = Resistor [tolerance=±5% resistance=220 package=THT]
  R9 = Resistor [tolerance=±5% resistance=220 package=THT]

nets:
  N1: S1.Pin_1, S1.Pin_2, S1.Pin_3, S1.Pin_4, R1.Pin_0, LED1.cathode, Part1.D2, LED2.cathode, LED3.cathode, LED4.cathode, LED5.cathode, LED6.cathode, LED7.cathode, LED8.cathode
  N2: LED1.anode, R4.Pin_0
  N3: Part1.D8, R5.Pin_1
  N4: Part1.D9_PWM, R6.Pin_1
  N5: Part1.D10_PWM/SS, R7.Pin_1
  N6: Part1.D11_PWM/MOSI, R8.Pin_1
  N7: Part1.D12/MISO, R9.Pin_1
  N8: Part1.D5_PWM, R2.Pin_1
  N9: Part1.D6_PWM, R3.Pin_1
  N10: Part1.D7, R4.Pin_1
  N11: LED2.anode, R5.Pin_0
  N12: LED3.anode, R6.Pin_0
  N13: LED4.anode, R7.Pin_0
  N14: LED5.anode, R8.Pin_0
  N15: LED6.anode, R9.Pin_0
  N16: LED7.anode, R3.Pin_0
  N17: LED8.anode, R2.Pin_0
