# Fritzing sketch id3891_Solarpowered_LEd_0 (saved by Fritzing 0.9.3b)
circuit board: 3cm x 2cm
breadboards: 1

parts:
  Inductors = Inductor [package="400 mil [THT]"]
  LED1 = LED - 5mm [color="Red (633nm)" package="5 mm [THT]"]
  LED2 = LED - 5mm [color="Red (633nm)" package="5 mm [THT]"]
  Inductor1 = Inductor [package="400 mil [THT]"]
  Battery = Battery
  Solar = Battery
  QX5252F = female pin header, 4 pins [form="♀ (female)"]

nets:
  N1: Inductors.pin_0, LED1.anode, LED2.anode, Inductor1.pin_0, QX5252F.pin4
  N2: Inductors.pin_1, Inductor1.pin_1, Battery.+, QX5252F.pin2
  GND: LED1.cathode, LED2.cathode, Battery.-, Solar.-, QX5252F.pin3
  N3: Solar.+, QX5252F.pin1

notes:
  Solar charged LED
  W.A. ten Brink
  +
  -
