# Fritzing sketch id3892_4xPhotoResistor_0 (saved by Fritzing 0.8.7b)
circuit board: 5.56378cm x 2.8cm
breadboards: 1

parts:
  10K_-_TL = Resistor [tolerance=±20% resistance=10k package=THT]
  10K_-_TR = Resistor [tolerance=±20% resistance=10k package=THT]
  10K_-_BL = Resistor [tolerance=±20% resistance=10k package=THT]
  photoresistor_TL = Photocell (LDR) [package=THT]
  photoresistor_TR = Photocell (LDR) [package=THT]
  photoresistor_BL = Photocell (LDR) [package=THT]
  photoresistor_BR = Photocell (LDR) [package=THT]
  10K_-_BR = Resistor [tolerance=±20% resistance=10k package=THT]

nets:
  GND: 10K_-_TL.Pin_0, 10K_-_TR.Pin_0, 10K_-_BL.Pin_0, 10K_-_BR.Pin_0
  N1: 10K_-_TL.Pin_1, photoresistor_TL.pin_0
  N2: 10K_-_TR.Pin_1, photoresistor_TR.pin_0
  N3: 10K_-_BL.Pin_1, photoresistor_BL.pin_0
  5V: photoresistor_TL.pin_1, photoresistor_TR.pin_1, photoresistor_BL.pin_1, photoresistor_BR.pin_1
  N4: photoresistor_BR.pin_0, 10K_-_BR.Pin_1

notes:
  TL
  TR
  BR
  BL
  Gnd
  +Vcc
