# Fritzing sketch id3893_solar_tracker_0 (saved by Fritzing 0.9.3b)
breadboards: 1

parts:
  R1 = Resistor [tolerance=±5% resistance=4.7k package=THT]
  R2 = Resistor [tolerance=±5% resistance=4.7k package=THT]
  LDR2 = Photocell (LDR) [package=THT]
  J1 = Basic Servo
  Part1 = Arduino Uno (Rev3)
  LDR1 = Photocell (LDR) [package=THT]
  C1_=_470uF = Electrolytic Capacitor [capacitance=1µF package="100 mil [THT, electrolytic]"]

nets:
  GND: R1.Pin_0, R2.Pin_0, J1.gnd, Part1.GND, C1_=_470uF.-
  N1: R1.Pin_1, Part1.A0, LDR1.pin_0
  N2: R2.Pin_1, LDR2.pin_0, Part1.A1
  VCC: LDR2.pin_1, J1.vcc, Part1.5V, LDR1.pin_1, C1_=_470uF.+
  N3: J1.pulse, Part1.D11_PWM/MOSI
