# Fritzing sketch id3894_Solenoide_0 (saved by Fritzing 0.9.3b)
breadboards: 1

parts:
  Componente1 = Arduino Uno (Rev3)
  Power_plug1 = Power plug
  L1 = Solenoid
  R2 = Resistor [tolerance=±5% resistance=1k package="2010 [SMD]"]
  D1 = Rectifier Diode [part_number=1N4001 package="Melf DO-213 AB [SMD]"]
  Q2 = TIP120_Hi_Current_Darlington_Transistor

nets:
  N1: Componente1.D13/SCK, R2.Pin_1
  GND: Componente1.GND, Power_plug1.GND, Q2.connector3
  N2: Power_plug1.VCC, L1.pin2, D1.cathode
  N3: L1.pin1, D1.anode, Q2.connector2
  N4: R2.Pin_0, Q2.connector1

notes:
  Solenoid JF-0530b
  12V
