# Fritzing sketch id3895_SharableSonar_Sampler_0 (saved by Fritzing 0.3.8b)

parts:
  Arduino1 = Arduino
  X1 = Sonar
  U1 = SPI Serial EEPROM
  R2 = 10k Ω Resistor [package=THT]
  R4 = 10k Ω Resistor [package=THT]
  S1 = Pushbutton [package=THT]

nets:
  N1: Arduino1.GND, X1.connector4, U1.connector3, R4.Pin_0
  N2: Arduino1.D13, U1.connector5
  N3: Arduino1.D12, U1.connector1
  N4: Arduino1.D11, U1.connector4
  N5: Arduino1.D10, U1.connector0
  N6: Arduino1.D4, R4.Pin_1, S1.Pin_3, S1.Pin_4
  N7: Arduino1.+5V, X1.connector0, U1.connector7, R2.Pin_1, S1.Pin_1, S1.Pin_2
  N8: Arduino1.A4, X1.connector1
  N9: Arduino1.A5, X1.connector2
  N10: U1.connector2, U1.connector6, R2.Pin_0
