# Fritzing sketch id3898_SONIDO_PIRATA_EL_CARIBE_0 (saved by Fritzing 0.9.2b)
breadboards: 1

parts:
  Parte1 = Arduino Uno (Rev3)
  J2 = Piezo Speaker
  LED1 = smd LED [color="Red (633nm)" package="1206 [SMD]"]
  R1 = Resistor [tolerance=±5% resistance=220 package=THT]
  R2 = Resistor [tolerance=±5% resistance=220 package=THT]
  LED2 = smd LED [color="Red (633nm)" package="1206 [SMD]"]

nets:
  N1: Parte1.D9_PWM, J2.pin2
  N2: Parte1.GND, R1.Pin_0, R2.Pin_0
  N3: Parte1.D4, LED2.cathode
  N4: Parte1.D6_PWM, LED1.cathode
  N5: LED1.anode, R1.Pin_1
