# Fritzing sketch id389_Alarma_Basica_0 (saved by Fritzing 0.9.2b)
breadboards: 1

parts:
  LCD1 = LCD screen
  Parte1 = Arduino Uno (Rev3)
  Matrix_keypad1 = CMG
  J1 = Piezo Speaker
  R1 = Rotary Potentiometer (Small) [maximum_resistance=100kΩ package=THT]
  LED1 = LED - 3mm [color="Red (633nm)" package="3 mm [THT]"]
  LED2 = LED - 3mm [color="Blue (430nm)" package="3 mm [THT]"]
  R2 = Resistor [tolerance=±5% resistance=330 package=THT]
  R3 = Resistor [tolerance=±5% resistance=330 package=THT]
  PIR1 = PIR_sensor

nets:
  VSS: LCD1.VSS, LCD1.R/W, LCD1.LED-, Parte1.GND, J1.pin1, R1.leg1, LED1.cathode, LED2.cathode, PIR1.connector3
  VDD: LCD1.VDD, LCD1.LED+, Parte1.5V, R1.leg2, PIR1.connector1
  N1: LCD1.V0, R1.wiper
  N2: LCD1.RS, Parte1.D5_PWM
  N3: LCD1.E, Parte1.D4
  N4: LCD1.DB4, Parte1.D3_PWM
  N5: LCD1.DB5, Parte1.D2
  N6: LCD1.DB6, Parte1.D1/TX
  N7: LCD1.DB7, Parte1.D0/RX
  N8: Parte1.A0, PIR1.connector2
  N9: Parte1.A1, J1.pin2
  N10: Parte1.A2, R2.Pin_1
  N11: Parte1.A3, R3.Pin_1
  N12: Parte1.D8, Matrix_keypad1.connector30
  N13: Parte1.D9_PWM, Matrix_keypad1.connector29
  N14: Parte1.D10_PWM/SS, Matrix_keypad1.connector28
  N15: Parte1.D11_PWM/MOSI, Matrix_keypad1.connector27
  N16: Parte1.D12/MISO, Matrix_keypad1.connector26
  N17: Parte1.D13/SCK, Matrix_keypad1.connector25
  N18: Parte1.D6_PWM, Matrix_keypad1.connector32
  N19: Parte1.D7, Matrix_keypad1.connector31
  N20: LED1.anode, R2.Pin_0
  N21: LED2.anode, R3.Pin_0

notes:
  Visit: https://github.com/proyectoTEOS/Alarma_Basica
