# Fritzing sketch id38_15witchedled_0 (saved by Fritzing 0.9.3b)
circuit board: 3.01055cm x 2.9799cm
breadboards: 1

parts:
  VCC1 = Battery block 9V
  LED1 = LED - 3mm [color="Red (633nm)" package="3 mm [THT]"]
  C2 = Electrolytic Capacitor [capacitance=10µF package="100 mil [THT, electrolytic]"]
  R4 = Resistor [tolerance=±5% resistance=220 package=THT]
  R2 = Resistor [tolerance=±5% resistance=6.8k package=THT]
  U1 = 555 Timer [package="DIP8 [THT]"]
  R3 = Resistor [tolerance=±5% resistance=16k package=THT]

nets:
  N1: VCC1.-, C2.-, U1.Ground
  N2: VCC1.+, LED1.anode, R2.Pin_1, U1.Reset, U1.Vcc_Supply_Voltage
  N3: LED1.cathode, R4.Pin_0
  N4: C2.+, U1.Trigger, U1.Threshold, R3.Pin_0
  N5: R4.Pin_1, U1.Output
  N6: R2.Pin_0, U1.Discharge, R3.Pin_1

notes:
  Gioannetti
  M
  G
  Martin
  p4
