# Fritzing sketch id3902_sonido_con_arduino_0 (saved by Fritzing 0.7.10b)
breadboards: 1

parts:
  Arduino1 = Arduino
  J1 = Piezo Speaker

nets:
  N1: Arduino1.D9, J1.pin2
  N2: Arduino1.GND, J1.pin1

notes:
  Melody Project with Arduino (Jing)
