# Fritzing sketch id3903_Sonnette_simple_0 (saved by Fritzing 0.9.2b)
breadboards: 1

parts:
  Composant1 = Arduino Uno (Rev3)
  J1 = Piezo Speaker  # not connected
  S1 = Pushbutton [package="[THT]"]
  R1 = Resistor [tolerance=±5% resistance=220 package=THT]

nets:
  N1: Composant1.D2, S1.Pin_3, S1.Pin_4, R1.Pin_0
  N2: Composant1.5V, S1.Pin_1, S1.Pin_2
  N3: Composant1.GND, R1.Pin_1
