# Fritzing sketch id3905_HarvestDemo_0 (saved by Fritzing 0.9.3b)
breadboards: 1

parts:
  hc-sr1 = hc-sr04
  S9 = Round Pushbutton
  Raspberry_Pi_1 = Raspberry Pi 3 [part_number=RPI-3-V1.2]
  DS1 = DS18B20 1-Wire Temperature Sensor [part_number=DS18B20]
  R1 = Resistor [tolerance=±5% resistance=220 package=THT]

nets:
  VCC: hc-sr1.VCC, Raspberry_Pi_1.5V
  N1: hc-sr1.Trig, Raspberry_Pi_1.GPIO17
  N2: hc-sr1.Echo, Raspberry_Pi_1.GPIO27
  GND: hc-sr1.GND, S9.leg0, Raspberry_Pi_1.GND, DS1.GND
  N3: S9.leg1, Raspberry_Pi_1.GPIO18
  3V3: Raspberry_Pi_1.3v3, DS1.VDD, R1.Pin_1
  N4: Raspberry_Pi_1.GPIO4, DS1.DQ, R1.Pin_0
