# Fritzing sketch id3906_Project_2___SOS_Morse_Code_Signaler_0 (saved by Fritzing 0.9.0b)
breadboards: 1

parts:
  Part1 = Arduino Uno (Rev3)
  R1 = Resistor [tolerance=±5% resistance=220 package=THT]
  LED1 = LED - 5mm [color="Green (565nm)" package="5 mm [THT]"]
  LED2 = LED - 5mm [color="Yellow (595nm)" package="5 mm [THT]"]
  LED3 = LED - 5mm [color="Blue (430nm)" package="5 mm [THT]"]
  S1 = Pushbutton [package="[THT]"]
  R2 = Resistor [tolerance=±5% resistance=220 package=THT]
  R3 = Resistor [tolerance=±5% resistance=220 package=THT]
  J1 = Piezo Speaker

nets:
  N1: Part1.D8, S1.Pin_3, S1.Pin_4
  N2: Part1.GND, LED1.cathode, LED2.cathode, LED3.cathode, J1.pin1
  N3: Part1.D2, R3.Pin_1
  N4: Part1.D4, R2.Pin_1
  N5: Part1.D6_PWM, R1.Pin_1
  N6: R1.Pin_0, LED3.anode
  N7: LED1.anode, R3.Pin_0
  N8: LED2.anode, R2.Pin_0
  N9: S1.Pin_1, S1.Pin_2, J1.pin2

notes:
  Components REQD:
  1) Arduino UNO
  2) Jumper Wires
  3) LED [x3]
  4) 220 Ohm Resistors [x3]
  5) Buzzer 5V [x1]
  6) Pushbutton
