# Fritzing sketch id3907_Sound_Boy_0 (saved by Fritzing 0.9.2b)
stripboards: 8
perfboards: 1

parts:
  TRS1 = Audio Jack (TRS) 3.5mm [package="4Ucon 08780 [THT]"]
  JP1 = RCA [package=rca_lock]
  JP2 = RCA [package=rca_lock]
  SPKR1 = Loudspeaker
  SPKR2 = Loudspeaker
  R1 = Rotary Potentiometer (Large) [maximum_resistance=100kΩ package=THT]  # not connected
  S1 = Toggle Switch [package=THT]
  R2 = Resistor [tolerance=±5% resistance=470 package=THT]
  LED1 = LED - 5mm [color="Green (560nm)" package="5 mm [THT]"]
  LED3 = LED - 5mm [color="Red (633nm)" package="5 mm [THT]"]
  J1 = Power Jack [package=power_jack_combo]
  U1 = Voltage Regulator - 5V [package="TO220 [THT]"]
  C1 = Ceramic Capacitor [capacitance=100nF package="100 mil [THT, multilayer]"]
  R3 = Resistor [tolerance=±5% resistance=470 package=THT]
  R4 = Resistor [tolerance=±5% resistance=2.2k package=THT]
  Q1 = NPN-Transistor [part_number=BC547 package="TO92 [THT]"]
  R6 = Trimmer Potentiometer [maximum_resistance=10kΩ package=THT]
  VCC2 = 4 x AAA Battery Mount
  R7 = Resistor [tolerance=±5% resistance=2.2k package=THT]
  C10 = Ceramic Capacitor [capacitance=100nF package="100 mil [THT, multilayer]"]

nets:
  N1: TRS1.Sleeve, TRS1.Ring, TRS1.Tip, JP1.PIN, JP1.SHELL, JP2.PIN, JP2.SHELL, SPKR1.pin1, SPKR1.pin2, SPKR2.pin2, R2.Pin_1, R4.Pin_1, Q1.B, VCC2.-, R7.Pin_1, C10.1
  N2: SPKR2.pin1, S1.L1, LED1.anode
  N3: S1.COM, U1.GND, R3.Pin_1, VCC2.+, C10.0
  N4: R2.Pin_0, LED1.cathode
  N5: LED3.cathode, Q1.C
  N6: LED3.anode, U1.input_voltage, R3.Pin_0, R6.leg1, R6.wiper
  N7: J1.GND, C1.1, Q1.E, R7.Pin_0
  N8: J1.PWR, U1.output_voltage, C1.0
  N9: R4.Pin_0, R6.leg2

notes:
  Sound input
  Mini-D 2 x 10watt Class-D Amplifier Kit
  Cat No: KC5530
  Jaycar
  Left in
  Right in
  Power
  left out
  right out
  Left RCA - white
  right RCA - red
  3.5mm stereo
  power input 2.1
  double gang volume
  log
  speaker output
  AS3032
  Batttery Pack
  8 aa
  PH9209
  charging circuit
  power circuit
  green led -SL2612
  Please check the code for the parts list
