# Fritzing sketch id3908_sound_detector___Copy_0 (saved by Fritzing 0.9.3b)
breadboards: 1

parts:
  Arduino_Nano = Arduino Nano (Rev3.0) (ICSP)
  R1 = Resistor [tolerance=±5% resistance=220 package=THT]
  LED1 = LED - 5mm [color="Red (633nm)" package="5 mm [THT]"]
  LM393_Sound_Sensor = Breakout Board for Electret Microphone

nets:
  GND: Arduino_Nano.GND, R1.Pin_1, LM393_Sound_Sensor.GND
  N1: Arduino_Nano.D4, LM393_Sound_Sensor.VCC
  N2: Arduino_Nano.D5, LED1.anode
  N3: Arduino_Nano.5V, LM393_Sound_Sensor.AUD
  N4: R1.Pin_0, LED1.cathode
