# Fritzing sketch id3910_sensor2_0 (saved by Fritzing 0.9.1b)
breadboards: 1

parts:
  Part2 = Arduino Uno (Rev3)
  LED1 = LEDs [package=led10mm]

nets:
  N1: Part2.D9_PWM, LED1.A
  N2: Part2.VIN, LED1.C
