# Fritzing sketch id3912_Sound_Wave_Start_Gun_0 (saved by Fritzing 0.9.3b)

parts:
  Part2 = Breakout Board for Electret Microphone
  U1 = Vibration Motor- ROB-08449 [package=vibe-motor-10mm]
  Part1 = Arduino Nano (Rev3.0) (ICSP)

nets:
  VCC: Part2.VCC, Part1.5V
  GND: Part2.GND, U1.+, Part1.GND
  N1: Part2.AUD, Part1.A2
  N2: U1.-, Part1.D3
