# Fritzing sketch id3917_SpaceShip_Interface_0 (saved by Fritzing 0.9.2b)
breadboards: 1

parts:
  Part1 = Arduino Uno (Rev3)
  R1 = Resistor [tolerance=±5% resistance=10k package=THT]
  R2 = Resistor [tolerance=±5% resistance=220 package=THT]
  R3 = Resistor [tolerance=±5% resistance=220 package=THT]
  R4 = Resistor [tolerance=±5% resistance=220 package=THT]
  S_1 = Pushbutton [package="[THT]"]
  LED_1 = LED - 5mm [color="Red (633nm)" package="5 mm [THT]"]
  LED_2 = LED - 5mm [color="Yellow (585nm)" package="5 mm [THT]"]
  LED_3 = LED - 5mm [color="Green (555nm)" package="5 mm [THT]"]

nets:
  N1: Part1.D2, R1.Pin_0, S_1.Pin_1, S_1.Pin_2
  N2: Part1.D3_PWM, LED_3.anode
  N3: Part1.D4, LED_2.anode
  N4: Part1.D5_PWM, LED_1.anode
  N5: Part1.5V, R1.Pin_1, S_1.Pin_3, S_1.Pin_4
  N6: Part1.GND, R2.Pin_1, R3.Pin_1, R4.Pin_1
  N7: R2.Pin_0, LED_2.cathode
  N8: R3.Pin_0, LED_3.cathode
  N9: R4.Pin_0, LED_1.cathode

notes:
  Engines OK
  Check Engine
  Engine Failure Critical
