# Fritzing sketch id3918_SpaceBucket_v1_0 (saved by Fritzing 0.9.3b)
circuit board: 9.15108cm x 6.25925cm
breadboards: 1

parts:
  RHT1 = Humidity and Temperature Sensor RHT03
  Part2 = Soil Moisture Sensor
  R1 = PHOTOCELL [package=photocell-kit]
  R2 = Resistor [tolerance=±5% resistance=4.7k package="0603 [SMD]"]
  Part1 = Arduino Uno (Rev3) - ICSP
  U2 = ESP8266_module [part_number=ESP8266]

nets:
  VCC: RHT1.Vcc, R1.P$1, Part1.5V
  N1: RHT1.Data-signal, Part1.D2
  GND: RHT1.GND_1, RHT1.GND_2, Part2.GND, R2.Pin_1, Part1.GND
  N2: Part2.VCC, Part1.D3_PWM
  N3: Part2.SIG, Part1.A1
  N4: R1.P$2, R2.Pin_0, Part1.A0
  N5: Part1.D0/RX, U2.connector7
  N6: Part1.D1/TX, U2.connector0
  N7: U2.connector1, U2.connector5
  N8: U2.connector6, U2.connector12
