# Fritzing sketch id3919_ElekSchema (saved by Fritzing 0.9.3b)
breadboards: 1

parts:
  Arduino_Uno1 = Arduino Uno (Rev3)
  LED1 = LED - 5mm [color="Red (633nm)" package="5 mm [THT]"]
  J2 = Infrared Proximity Sensor
  J1 = Infrared Proximity Sensor

nets:
  N1: Arduino_Uno1.A0, J2.Vout
  N2: Arduino_Uno1.A1, J1.Vout
  N3: Arduino_Uno1.D13/SCK, LED1.anode
  VCC: Arduino_Uno1.5V, J2.Vcc, J1.Vcc
  GND: Arduino_Uno1.GND, LED1.cathode, J2.GND, J1.GND
