# Fritzing sketch id3919_Saceship_Dashboard_v1.0_0 (saved by Fritzing 0.8.7b)
breadboards: 1

parts:
  Part1 = Arduino Uno (Rev3)
  S1 = Pushbutton [package="[THT]"]  # not connected
  R1 = Resistor [tolerance=±5% resistance=330 package=THT]
  R2 = Resistor [tolerance=±5% resistance=330 package=THT]
  LED1 = LED - 5mm [color="Green (555nm)" package="5 mm [THT]"]
  R3 = Resistor [tolerance=±5% resistance=100 package=THT]
  LED2 = LED - 5mm [color="Green (555nm)" package="5 mm [THT]"]
  R4 = Resistor [tolerance=±5% resistance=100 package=THT]
  R5 = Resistor [tolerance=±5% resistance=330 package=THT]
  LED3 = LED - 5mm [color="Red (633nm)" package="5 mm [THT]"]
  LED4 = LED - 5mm [color="Red (633nm)" package="5 mm [THT]"]
  R6 = Resistor [tolerance=±5% resistance=330 package=THT]
  LED5 = LED - 5mm [color="Yellow (585nm)" package="5 mm [THT]"]
  R7 = Resistor [tolerance=±5% resistance=330 package=THT]
  LED6 = LED - 5mm [color="Yellow (585nm)" package="5 mm [THT]"]
  R8 = Resistor [tolerance=±10% resistance=10k package=THT]
  S2 = Pushbutton [package="[THT]"]
  LED7 = LED - 5mm [color="Red (633nm)" package="5 mm [THT]"]
  R9 = Resistor [tolerance=±5% resistance=330 package=THT]
  R10 = Resistor [tolerance=±10% resistance=10k package=THT]
  LED8 = LED - 5mm [color="Red (633nm)" package="5 mm [THT]"]
  R11 = Resistor [tolerance=±10% resistance=10k package=THT]
  LED9 = LED - 5mm [color="Yellow (585nm)" package="5 mm [THT]"]

nets:
  N1: Part1.D8, LED7.cathode
  N2: Part1.D10_PWM/SS, LED8.cathode
  N3: Part1.D11_PWM/MOSI, LED9.cathode
  N4: Part1.D2, R1.Pin_0
  N5: Part1.D3_PWM, LED2.cathode
  N6: Part1.D4, LED3.cathode, LED4.cathode
  N7: Part1.D6_PWM, LED5.cathode, LED6.cathode
  N8: Part1.5V, R9.Pin_1, R10.Pin_1
  N9: Part1.GND, R1.Pin_1, R2.Pin_1, R3.Pin_0, R4.Pin_1, R5.Pin_0, R6.Pin_1, R7.Pin_0, R8.Pin_0
  N10: R2.Pin_0, LED1.cathode
  N11: LED1.anode, S2.Pin_3, S2.Pin_4
  N12: R3.Pin_1, LED2.anode
  N13: R4.Pin_0, LED4.anode
  N14: R5.Pin_1, LED3.anode
  N15: R6.Pin_0, LED5.anode
  N16: R7.Pin_1, LED6.anode
  N17: R8.Pin_1, LED7.anode
  N18: R10.Pin_0, LED8.anode
  N19: R11.Pin_0, LED9.anode
