# Fritzing sketch id391_AM2302MiniBreadboard_0 (saved by Fritzing 0.7.11b)
breadboards: 1

parts:
  Arduino1 = Arduino
  AM2302 = Humidity and Temperature Sensor RHT03

nets:
  N1: Arduino1.D2, AM2302.Data-signal
  +5V: Arduino1.+5V, AM2302.Vcc
  N2: Arduino1.GND, AM2302.GND_1, AM2302.GND_2

notes:
  Arduino Uno + AM2302 Sensor
  Derek Erb - 31/01/2013
  about.me/derekerb
  derek.erb@gmail.com
  AM2302 +5v power to Arduino 5v
  AM2302 Data to Arduino Pin 2 (or 3)
  AM2302 Supplementary ground to Arduino GND
  AM2302 Principal ground to Arduino GND
  AM2302 Left to right
  Sticker / Label facing up
