# Fritzing sketch id3920_spaceshipinterface_0 (saved by Fritzing 0.9.2b)
breadboards: 1

parts:
  Part1 = Arduino Uno (Rev3)
  R1 = Resistor [tolerance=±5% resistance=220 package=THT]
  R2 = Resistor [tolerance=±5% resistance=220 package=THT]
  R3 = Resistor [tolerance=±20% resistance=220 package=THT]
  R4 = Resistor [tolerance=±10% resistance=10k package=THT]
  S1 = Pushbutton [package="[THT]"]
  LED1 = LED - 5mm [color="Red (633nm)" package="5 mm [THT]"]
  LED2 = LED - 5mm [color="Red (633nm)" package="5 mm [THT]"]
  LED3 = LED - 5mm [color="Green (555nm)" package="5 mm [THT]"]

nets:
  N1: Part1.D2, R4.Pin_0, S1.Pin_1, S1.Pin_2
  N2: Part1.D3_PWM, LED3.anode
  N3: Part1.D4, LED2.anode
  N4: Part1.D5_PWM, LED1.anode
  N5: Part1.5V, S1.Pin_3, S1.Pin_4
  N6: Part1.GND, R1.Pin_1, R2.Pin_1, R3.Pin_1, R4.Pin_1
  N7: R1.Pin_0, LED3.cathode
  N8: R2.Pin_0, LED2.cathode
  N9: R3.Pin_0, LED1.cathode
