# Fritzing sketch id3922_Board_0 (saved by Fritzing 0.8.7b)
breadboards: 1

parts:
  Bauteil1 = Arduino Uno (Rev3)
  S1 = Pushbutton [package="[THT]"]
  R1 = Photocell (LDR) [package=THT]
  R2 = Resistor [tolerance=±5% resistance=220 package=THT]
  R3 = Resistor [tolerance=±5% resistance=220 package=THT]
  LED1 = LED - 5mm [color="Red (633nm)" package="5 mm [THT]"]
  R5 = Resistor [tolerance=±5% resistance=220 package=THT]

nets:
  N1: Bauteil1.A0, R1.pin_0, R2.Pin_1
  N2: Bauteil1.D2, LED1.anode
  N3: Bauteil1.D3_PWM, S1.Pin_1, S1.Pin_2, R3.Pin_0
  N4: Bauteil1.5V, S1.Pin_3, S1.Pin_4, R1.pin_1
  N5: Bauteil1.GND, R2.Pin_0, R3.Pin_1, R5.Pin_0
  N6: LED1.cathode, R5.Pin_1
