# Fritzing sketch id3923_TMP36_0 (saved by Fritzing 0.9.1b)
circuit board: 2.05cm x 4.6cm
breadboards: 1

parts:
  T1 = TMP36 Temperature Sensor [package="TO92 [THT]"]
  U2 = SPARKCORE
  C1 = Ceramic Capacitor [capacitance=2.2nF package="100 mil [THT, multilayer]"]
  C2 = Ceramic Capacitor [capacitance=2.2nF package="100 mil [THT, multilayer]"]

nets (from the pcb view):
  N1: T1.+Vs, U2.connector62, C2.1
  N2: T1.Vout, U2.connector41, C1.1
  N3: T1.GND, U2.connector51, C1.0, C2.0
