# Fritzing sketch id3924_iotoilet_0 (saved by Fritzing 0.8.8b)
circuit board: 5.41584cm x 3.15524cm

parts:
  L1 = Solenoid
  MOSFET = Basic FET P-Channel [package="TO220 [THT]"]
  Spark_Core = Spark Core (v1.0)
  Power_plug1 = Power plug
  VReg = Voltage Regulator - 5V [package="TO220 [THT]"]
  100k = Resistor [tolerance=±5% resistance=100k package=THT]
  D1 = Rectifier Diode [part_number=1N4001 breakdown_voltage=3.6V package="300 mil [THT]"]
  S1 = Tilt Switch [package=THT]
  10k = Resistor [tolerance=±5% resistance=10k package=THT]
  LED = LED - 5mm [color="Red (633nm)" package="5 mm [THT]"]
  220 = Resistor [tolerance=±5% resistance=220 package=THT]
  100n = Ceramic Capacitor [capacitance=100nF package="100 mil [THT, multilayer]"]
  47u = Electrolytic Capacitor [capacitance=47µF package="100 mil [THT, electrolytic]"]
  47u_2 = Electrolytic Capacitor [capacitance=47µF package="100 mil [THT, electrolytic]"]
  J1 = female pin header, 12 pins [form="♀ (female)"]
  J2 = female pin header, 12 pins [form="♀ (female)"]
  knock = Screw terminal - 2 pins [package=THT]
  lock = Screw terminal - 2 pins [package=THT]

nets:
  N1: L1.pin1, VReg.input_voltage, D1.cathode, 47u.+, knock.pin1
  N2: L1.pin2, MOSFET.drain, knock.pin2
  N3: MOSFET.gate, Spark_Core.D0, 100k.Pin_1, J2.pin1
  GND: MOSFET.source, Spark_Core.GND, Power_plug1.GND, VReg.GND, 100k.Pin_0, 10k.Pin_0, 220.Pin_0, 100n.0, 47u.-, 47u_2.-, J1.pin11, J2.pin9
  N4: Spark_Core.A0, J1.pin1
  N5: Spark_Core.A1, J1.pin2
  N6: Spark_Core.A2, J1.pin3
  N7: Spark_Core.A3, J1.pin4
  N8: Spark_Core.A4, J1.pin5
  N9: Spark_Core.A5, J1.pin6
  N10: Spark_Core.A6, J1.pin7
  N11: Spark_Core.A7, J1.pin8
  N12: Spark_Core.TX, J1.pin9
  N13: Spark_Core.RX, J1.pin10
  N14: Spark_Core.VIN, VReg.output_voltage, 100n.1, 47u_2.+, J1.pin12
  N15: Spark_Core.D1, J2.pin2
  N16: Spark_Core.D2, J2.pin3
  N17: Spark_Core.D3, J2.pin4
  N18: Spark_Core.D4, J2.pin5
  N19: Spark_Core.D5, LED.anode, J2.pin6
  N20: Spark_Core.D6, J2.pin7
  N21: Spark_Core.D7, S1.Pin_2, 10k.Pin_1, J2.pin8, lock.pin2
  N22: Spark_Core.3V3*, J2.pin10
  N23: Spark_Core.RST, J2.pin11
  N24: Spark_Core.3V3, S1.Pin_1, J2.pin12, lock.pin1
  N25: Power_plug1.VCC, D1.anode
  N26: LED.cathode, 220.Pin_1

notes:
  IoToilet
