# Fritzing sketch id3926_Sparkfun_Joystick_Shield_with_Arduino_Pro_Mini_and_XBee_0 (saved by Fritzing 0.9.2b)

parts:
  Part2 = Arduino Pro Mini v13
  Part3 = Arduino Joystick Shield
  Part4 = XBee Explorer Regulated
  Part5 = Power Cell LiPo Charger/Booster
  U1 = XBee  # not connected
  U2 = LIPO-1000mAh [package=lipo-1000]  # not connected

nets:
  N1: Part2.DTR, Part4.DIO3
  N2: Part2.D0/TX, Part4.DIN
  N3: Part2.D1/RX, Part4.DOUT
  VCC: Part2.VCC, Part4.5V
  GND: Part2.GND, Part4.GND, Part5.GND
  N4: Part2.RAW, Part5.VCC
  N5: Part2.A1, Part3.HORIZONTAL
  N6: Part2.A0, Part3.VERTICAL
  N7: Part2.D6_PWM, Part3.D6
  N8: Part2.D5_PWM, Part3.D5
  N9: Part2.D4, Part3.D4
  N10: Part2.D3_PWM, Part3.D3
  N11: Part2.D2, Part3.SEL
