# Fritzing sketch id3927_Speaker_0 (saved by Fritzing 0.9.3b)
circuit board: 8.46667cm x 5.64444cm
breadboards: 1

parts:
  R1 = Resistor [tolerance=±5% resistance=200 package=THT]
  R2 = Resistor [tolerance=±5% resistance=100 package=THT]
  SPKR1 = Loudspeaker
  Adafruit_HUZZAH_ESP8266_Breakout1 = Adafruit HUZZAH ESP8266 Breakout [part_number=2471]
  VCC1 = Battery  # not connected

nets:
  N1: R1.Pin_0, R2.Pin_1
  N2: R1.Pin_1, Adafruit_HUZZAH_ESP8266_Breakout1.#2
  N3: R2.Pin_0, SPKR1.pin2
  N4: SPKR1.pin1, Adafruit_HUZZAH_ESP8266_Breakout1.GND
