# Fritzing sketch id3928_PCB_Spectrumino_0 (saved by Fritzing 0.9.2b)
circuit board: 9.22482cm x 6.22957cm
breadboards: 1

parts:
  Pre-Assembled_Female_BNC1 = Pre-Assembled Female BNC
  Pre-Assembled_Female_BNC3 = Pre-Assembled Female BNC
  R1 = Resistor [tolerance=±5% resistance=470 package=THT]
  C1 = Ceramic Capacitor [capacitance=1µF package="100 mil [THT, multilayer]"]
  Pre-Assembled_Female_BNC2 = Pre-Assembled Female BNC
  Pre-Assembled_Female_BNC4 = Pre-Assembled Female BNC
  Pre-Assembled_Female_BNC5 = Pre-Assembled Female BNC
  U1 = RS232 Transceiver [package=dil16]
  U2 = RS232 Transceiver [package=dil16]
  X1 = DB9 Connector [package=db9]
  X2 = DB9 Connector [package=db9]
  C2 = Electrolytic Capacitor [capacitance=100nF package="100 mil [THT, electrolytic]"]
  C3 = Electrolytic Capacitor [capacitance=100nF package="100 mil [THT, electrolytic]"]
  C4 = Electrolytic Capacitor [capacitance=100nF package="100 mil [THT, electrolytic]"]
  C5 = Electrolytic Capacitor [capacitance=100nF package="100 mil [THT, electrolytic]"]
  C6 = Electrolytic Capacitor [capacitance=100nF package="100 mil [THT, electrolytic]"]
  C7 = Electrolytic Capacitor [capacitance=100nF package="100 mil [THT, electrolytic]"]
  C8 = Electrolytic Capacitor [capacitance=100nF package="100 mil [THT, electrolytic]"]
  C9 = Electrolytic Capacitor [capacitance=100nF package="100 mil [THT, electrolytic]"]
  C10 = Electrolytic Capacitor [capacitance=100nF package="100 mil [THT, electrolytic]"]
  C11 = Electrolytic Capacitor [capacitance=100nF package="100 mil [THT, electrolytic]"]
  JP1 = Header 6 [package=1x06-smd]
  JP2 = Header 6 [package=1x06-smd]

nets:
  N1: Pre-Assembled_Female_BNC1.PRB, JP1.3
  GND: Pre-Assembled_Female_BNC1.GND, Pre-Assembled_Female_BNC3.GND, C1.1, Pre-Assembled_Female_BNC2.GND, Pre-Assembled_Female_BNC4.GND, Pre-Assembled_Female_BNC5.GND, X1.5, X2.5, C4.+, C5.-, C9.+, C10.-, JP1.2
  N2: Pre-Assembled_Female_BNC3.PRB, R1.Pin_1, C1.0
  N3: R1.Pin_0, JP1.5
  N4: Pre-Assembled_Female_BNC2.PRB, JP1.4
  N5: Pre-Assembled_Female_BNC4.PRB, JP2.1
  N6: Pre-Assembled_Female_BNC5.PRB, JP2.2
  N7: U1.C1+, C2.+
  N8: U1.V+, C6.+
  N9: U1.C1-, C2.-
  N10: U1.C2+, C3.+
  N11: U1.C2-, C3.-
  N12: U1.V-, C4.-
  N13: U1.T1IN, JP2.5
  N14: U1.R1OUT, JP2.6
  N15: U1.R1IN, X1.2
  N16: U1.T1OUT, X1.3
  VCC: U1.VCC, U2.VCC, C5.+, C6.-, C10.+, C11.-, JP1.1
  N17: U2.C1+, C7.+
  N18: U2.V+, C11.+
  N19: U2.C1-, C7.-
  N20: U2.C2+, C8.+
  N21: U2.C2-, C8.-
  N22: U2.V-, C9.-
  N23: U2.T1IN, JP2.3
  N24: U2.R1OUT, JP2.4
  N25: U2.R1IN, X2.2
  N26: U2.T1OUT, X2.3

notes:
  pow.met
  PKLS
  ECG
  TTLframe
  shutter
  PC
  laser
  6
  A
  B
  3.3V
  GND
  A0
  A5
  DAC0
  none
  pin 5
  pin 8
  pin 14
  pin 15
  pin 18
  pin 19
