# Fritzing sketch id3929_Motor_Project_0 (saved by Fritzing 0.9.3b)
breadboards: 1

parts:
  Part1 = Arduino Uno (Rev3)
  Q1 = NPN-Transistor [package="TO92 [THT]"]
  R1 = Resistor [tolerance=±5% resistance=220 package=THT]
  U1 = Voltage Regulator - 5V [package="DPak [SMD]"]
  D1 = Rectifier Diode [part_number=1N4001 package="300 mil [THT]"]
  M1 = DC Motor
  VCC1 = Battery block 9V  # not connected
  Part2 = Max Power IR LED Kit

nets:
  N1: Part1.D9_PWM, R1.Pin_0
  N2: Part1.D2, Part2.CONTROL
  5V: Part1.5V, Part2.VCC
  GND: Part1.GND, Q1.E, U1.GND, Part2.GND
  N3: Q1.B, R1.Pin_1
  N4: Q1.C, D1.anode, M1.pin_2
  N5: U1.output_voltage, D1.cathode, M1.pin_1
