# Fritzing sketch id392_ArduinoAm29F010_arduinouno_0 (saved by Fritzing 0.9.0b)
circuit board: 6.88566cm x 5.36311cm
breadboards: 4

parts:
  Arduino_Uno = arduinouno
  IC1 = IC, DIP package, 20 pins [chip_label=M74HC273B1 part_number=M74HC273B1]
  IC2 = IC, DIP package, 20 pins [chip_label=M74HC273B1 part_number=M74HC273B1]
  U2 = dil32

nets (from the pcb view):
  N1: Arduino_Uno.connector2, U2.connector1
  N2: Arduino_Uno.connector3, U2.connector30
  N3: Arduino_Uno.connector4, U2.connector23
  N4: Arduino_Uno.connector5, U2.connector21
  N5: Arduino_Uno.connector51, IC1.pin13, IC2.pin13, U2.connector17
  N6: Arduino_Uno.connector52, IC1.pin14, IC2.pin14, U2.connector18
  N7: Arduino_Uno.connector53, IC1.pin17, IC2.pin17, U2.connector19
  N8: Arduino_Uno.connector54, IC1.pin18, IC2.pin18, U2.connector20
  N9: Arduino_Uno.connector57, IC2.pin10
  N10: Arduino_Uno.connector63, IC1.pin11
  N11: Arduino_Uno.connector64, IC2.pin11
  N12: Arduino_Uno.connector65, IC1.pin8, IC2.pin8, U2.connector16
  N13: Arduino_Uno.connector66, IC1.pin7, IC2.pin7, U2.connector14
  N14: Arduino_Uno.connector67, IC1.pin4, IC2.pin4, U2.connector13
  N15: Arduino_Uno.connector68, IC1.pin3, IC2.pin3, U2.connector12
  N16: Arduino_Uno.connector87, IC1.pin1, IC1.pin20, IC2.pin1, IC2.pin20, U2.connector31
  N17: Arduino_Uno.connector89, IC1.pin10, U2.connector15
  N18: IC1.pin2, U2.connector11
  N19: IC1.pin5, U2.connector10
  N20: IC1.pin6, U2.connector9
  N21: IC1.pin9, U2.connector8
  N22: IC1.pin12, U2.connector7
  N23: IC1.pin15, U2.connector6
  N24: IC1.pin16, U2.connector5
  N25: IC1.pin19, U2.connector4
  N26: IC2.pin2, U2.connector26
  N27: IC2.pin5, U2.connector25
  N28: IC2.pin6, U2.connector22
  N29: IC2.pin9, U2.connector24
  N30: IC2.pin12, U2.connector3
  N31: IC2.pin15, U2.connector27
  N32: IC2.pin16, U2.connector28
  N33: IC2.pin19, U2.connector2
