# Fritzing sketch id3930_S4_FC_48_pin_0 (saved by Fritzing 0.9.3b)
circuit board: 4.5cm x 10cm
breadboards: 1

parts:
  Part3 = 174917_DENSO-ECU-socket_48pin-040-070 [part_number=174917 package="48-pin 0.40/0.70"]
  J3 = screw terminal, 2 pins
  J1 = shrouded pin header, 40 pins [form="♂ (shrouded male)"]

nets:
  12V: Part3.1A, Part3.1B, J3.pin2
  GND: Part3.1C, Part3.1D, Part3.2G, Part3.2H, Part3.2I, Part3.2J, J3.pin1, J1.pin9, J1.pin10, J1.pin12, J1.pin18, J1.pin23, J1.pin29
  Crank -: Part3.1G, J1.pin27
  Cam -: Part3.1I, J1.pin26
  TPS: Part3.1J, J1.pin22
  Crank +: Part3.1K, J1.pin25
  Cam +: Part3.1M, J1.pin24
  O2: Part3.1O, J1.pin21
  IAT: Part3.1S, J1.pin20
  Coolant: Part3.1V, J1.pin19
  5V Ref: Part3.2A, J1.pin13, J1.pin28
  MAP: Part3.2C, J1.pin11
  IGN3: Part3.2N, J1.pin33
  IGN1: Part3.2O, J1.pin7
  IGN2: Part3.2R, J1.pin34
  INJ4: Part3.2S, J1.pin6
  INJ3: Part3.2U, J1.pin4
  INJ2: Part3.2W, J1.pin2
  Boost: Part3.2X, J1.pin35
  INJ1: Part3.2Y, J1.pin1
  Idle: Part3.2Z, J1.pin37

notes:
  1A
  2A
  48-pin OEM ECU Connector
  Speeduino - S4 FC for v0.4
