# Fritzing sketch id3932_spi2sd_0 (saved by Fritzing 0.8.5b)
circuit board: 1.43075cm x 1.22647cm
breadboards: 1

parts:
  microSD = custom
  Pad1 = Pad [width=1.68 height=0.88 connect=center]
  Pad2 = Pad [width=1.68 height=0.88 connect=center]
  Pad3 = Pad [width=1.68 height=0.88 connect=center]
  Pad4 = Pad [width=1.68 height=0.88 connect=center]
  Pad5 = Pad [width=1.68 height=0.88 connect=center]
  Pad6 = Pad [width=1.68 height=0.88 connect=center]
  SPI = double row female pin header, 6 pins [form="♀ (female)"]
  C1 = Ceramic Capacitor [capacitance=10µF package="1206 [SMD, multilayer]"]
  C2 = Ceramic Capacitor [capacitance=10µF package="0805 [SMD, multilayer]"]

nets (from the pcb view):
  N1: microSD.connector1, Pad6.pad, SPI.pin3
  N2: microSD.connector2, Pad2.pad, SPI.pin5
  N3: microSD.connector3, Pad1.pad, SPI.pin6, C1.0, C2.0
  N4: microSD.connector4, Pad5.pad, SPI.pin2
  N5: microSD.connector5, microSD.connector8, microSD.connector9, Pad3.pad, SPI.pin4, C1.1, C2.1
  N6: microSD.connector6, Pad4.pad, SPI.pin1

notes:
  SPI2SD
