# Fritzing sketch id3933_SPICE_0 (saved by Fritzing 0.9.2b)
breadboards: 2

parts:
  Part1 = Arduino Nano (Rev3.0)
  S1 = Pushbutton [package="[THT]"]
  S2 = Pushbutton [package="[THT]"]
  S3 = Pushbutton [package="[THT]"]
  R1 = Resistor [tolerance=±5% resistance=1M package=THT]
  R2 = Resistor [tolerance=±5% resistance=1k package=THT]
  Q1 = NPN-Transistor [part_number=3904 package="TO92 [THT]"]
  Q2 = NPN-Transistor [part_number=3904 package="TO92 [THT]"]
  LED2 = LED - 5mm [color="Green (570nm)" package="5 mm [THT]"]
  LED3 = LED - 5mm [color="Red (633nm)" package="5 mm [THT]"]
  Q3 = NPN-Transistor [part_number=3904 package="TO92 [THT]"]
  LED4 = LED - 5mm [color="Blue (470nm)" package="5 mm [THT]"]
  R3 = Resistor [tolerance=±5% resistance=1k package=THT]
  R4 = Resistor [tolerance=±5% resistance=220 package=THT]
  R5 = Resistor [tolerance=±5% resistance=1k package=THT]
  R6 = Resistor [tolerance=±5% resistance=220 package=THT]
  R7 = Resistor [tolerance=±5% resistance=220 package=THT]
  R9 = Resistor [tolerance=±5% resistance=1k package=THT]
  LED6 = RGB LED - (4 legs) [package="5 mm [THT]"]
  Q7 = NPN-Transistor [part_number=3904 package="TO92 [THT]"]
  R14 = Resistor [tolerance=±5% resistance=1k package=THT]
  R16 = Resistor [tolerance=±5% resistance=220 package=THT]
  R18 = Resistor [tolerance=±5% resistance=220 package=THT]
  Q8 = NPN-Transistor [part_number=3904 package="TO92 [THT]"]
  R19 = Resistor [tolerance=±5% resistance=220 package=THT]
  LED7 = LED - 5mm [color="Red (633nm)" package="5 mm [THT]"]
  LED8 = LED - 5mm [color="Red (633nm)" package="5 mm [THT]"]
  LED9 = LED - 5mm [color="Red (633nm)" package="5 mm [THT]"]
  LED10 = LED - 5mm [color="Red (633nm)" package="5 mm [THT]"]
  LED11 = LED - 5mm [color="Yellow (592nm)" package="5 mm [THT]"]
  LED12 = LED - 5mm [color="Yellow (592nm)" package="5 mm [THT]"]
  LED13 = LED - 5mm [color="Yellow (592nm)" package="5 mm [THT]"]
  LED14 = LED - 5mm [color="Yellow (592nm)" package="5 mm [THT]"]
  LED16 = LED - 5mm [color="Blue (470nm)" package="5 mm [THT]"]
  LED17 = LED - 5mm [color="Blue (470nm)" package="5 mm [THT]"]
  LED18 = LED - 5mm [color="Blue (470nm)" package="5 mm [THT]"]
  LED19 = LED - 5mm [color="Blue (470nm)" package="5 mm [THT]"]
  LED20 = LED - 5mm [color="Green (570nm)" package="5 mm [THT]"]
  LED21 = LED - 5mm [color="Green (570nm)" package="5 mm [THT]"]
  LED22 = LED - 5mm [color="Green (570nm)" package="5 mm [THT]"]
  LED23 = LED - 5mm [color="Green (570nm)" package="5 mm [THT]"]
  R20 = Resistor [tolerance=±5% resistance=1k package=THT]
  R23 = Resistor [tolerance=±5% resistance=1k package=THT]
  R24 = Resistor [tolerance=±5% resistance=1k package=THT]
  R25 = Resistor [tolerance=±5% resistance=1k package=THT]
  R26 = Resistor [tolerance=±5% resistance=1k package=THT]
  R27 = Resistor [tolerance=±5% resistance=1k package=THT]
  R28 = Resistor [tolerance=±5% resistance=1k package=THT]
  R29 = Resistor [tolerance=±5% resistance=1k package=THT]
  R35 = Resistor [tolerance=±5% resistance=1k package=THT]
  R38 = Resistor [tolerance=±5% resistance=1k package=THT]
  R39 = Resistor [tolerance=±5% resistance=1k package=THT]
  R40 = Resistor [tolerance=±5% resistance=1k package=THT]
  R41 = Resistor [tolerance=±5% resistance=1k package=THT]
  R42 = Resistor [tolerance=±5% resistance=1k package=THT]
  R43 = Resistor [tolerance=±5% resistance=1k package=THT]
  IC3 = SHIFT REGISTER [package=dil16]
  R17 = Resistor [tolerance=±5% resistance=1k package=THT]
  R44 = Resistor [tolerance=±5% resistance=1k package=THT]
  Q6 = NPN-Transistor [part_number=3904 package="TO92 [THT]"]
  R45 = Resistor [tolerance=±5% resistance=1k package=THT]
  C1 = Electrolytic Capacitor [capacitance=1µF voltage=50V package="100 mil [THT, electrolytic]"]
  R46 = Rotary Potentiometer (Small) [maximum_resistance=10kΩ package=THT]
  R47 = Resistor [tolerance=±5% resistance=470 package=THT]
  Q9 = NPN-Transistor [package="TO92 [THT]"]
  R48 = Resistor [tolerance=±5% resistance=220 package=THT]
  IC2 = SHIFT REGISTER [package=dil16]
  LED1 = LED - 5mm [color="Red (633nm)" package="5 mm [THT]"]
  SPKR1 = Loudspeaker
  J1 = Piezo Speaker

nets:
  GND: Part1.GND, S1.Pin_3, S1.Pin_4, S2.Pin_3, S2.Pin_4, S3.Pin_3, S3.Pin_4, R1.Pin_0, IC3.GND, IC3.G, IC2.GND, IC2.G, J1.pin1
  N1: Part1.D10, IC2.SER
  N2: Part1.D11/MOSI, IC3.RCK, IC2.RCK
  N3: Part1.D12/MISO, IC3.SCK, IC2.SCK
  VIN: Part1.VIN, IC2.SCL, IC2.VCC
  N4: Part1.A0, R1.Pin_1, J1.pin2
  N5: Part1.D13/SCK, R48.Pin_0
  N6: S1.Pin_1, S1.Pin_2
  N7: S2.Pin_1, S2.Pin_2
  N8: S3.Pin_1, S3.Pin_2
  N9: R2.Pin_0, LED1.anode
  N10: Q1.E, Q2.E, Q3.E, Q7.E, Q8.E, R20.Pin_0, R23.Pin_0, R24.Pin_0, R25.Pin_0, R26.Pin_0, R27.Pin_0, R28.Pin_0, R29.Pin_0, R35.Pin_0, R38.Pin_0, R39.Pin_0, R40.Pin_0, R41.Pin_0, R42.Pin_0, R43.Pin_0, R44.Pin_0, Q6.E, Q9.E, SPKR1.pin2
  N11: Q1.B, R7.Pin_0
  N12: Q1.C, LED3.cathode
  N13: Q2.B, R6.Pin_0
  N14: Q2.C, LED2.cathode
  N15: LED2.anode, R5.Pin_1
  N16: LED3.anode, R45.Pin_1
  N17: Q3.B, R4.Pin_0
  N18: Q3.C, LED4.cathode
  N19: LED4.anode, R3.Pin_1
  N20: R3.Pin_0, R5.Pin_0, LED6.common_anode, R45.Pin_0, R47.Pin_1
  N21: R9.Pin_0, LED6.red_cathode
  N22: R9.Pin_1, Q6.C
  N23: LED6.green_cathode, R17.Pin_0
  N24: LED6.blue_cathode, R14.Pin_0
  N25: Q7.B, R16.Pin_0
  N26: Q7.C, R14.Pin_1
  N27: R18.Pin_0, Q8.B
  N28: Q8.C, R17.Pin_1
  N29: R19.Pin_0, Q6.B
  N30: LED7.cathode, R25.Pin_1
  N31: LED7.anode, IC2.QB
  N32: LED8.cathode, R23.Pin_1
  N33: LED8.anode, IC2.QC
  N34: LED9.cathode, R20.Pin_1
  N35: LED9.anode, IC2.QD
  N36: LED10.cathode, R44.Pin_1
  N37: LED10.anode, IC2.QA
  N38: LED11.cathode, R26.Pin_1
  N39: LED11.anode, IC2.QF
  N40: LED12.cathode, R24.Pin_1
  N41: LED12.anode, IC2.QE
  N42: LED13.cathode, R27.Pin_1
  N43: LED13.anode, IC2.QG
  N44: LED14.cathode, R28.Pin_1
  N45: LED14.anode, IC2.QH
  N46: LED16.cathode, R43.Pin_1
  N47: LED16.anode, IC3.QB
  N48: LED17.cathode, R29.Pin_1
  N49: LED17.anode, IC3.QA
  N50: LED18.cathode, R41.Pin_1
  N51: LED18.anode, IC3.QC
  N52: LED19.cathode, R42.Pin_1
  N53: LED19.anode, IC3.QD
  N54: LED20.cathode, R40.Pin_1
  N55: LED20.anode, IC3.QE
  N56: LED21.cathode, R39.Pin_1
  N57: LED21.anode, IC3.QF
  N58: LED22.cathode, R38.Pin_1
  N59: LED22.anode, IC3.QG
  N60: LED23.cathode, R35.Pin_1
  N61: LED23.anode, IC3.QH
  N62: IC3.SER, IC2.QH*
  N63: C1.-, SPKR1.pin1
  N64: C1.+, R46.leg2, Q9.C
  N65: R46.wiper, R47.Pin_0
  N66: Q9.B, R48.Pin_1
