# Fritzing sketch id3934_tinyEMF_0 (saved by Fritzing 0.9.3b)
circuit board: 6.16908cm x 3.67463cm
breadboards: 1

parts:
  AUDIO = 3.5mm Audio Jack [package=audio-jack-3.5mm-smd]
  HEADER_-_POWER = Header 2 [package=jst-2-pth]
  RED_LED = LED - 5mm [color="Red (633nm)" package="5 mm [THT]"]
  ATTINY85 = attiny85 [package=dip]
  MOSFET = Basic FET N-Channel [package="TO220 [THT]"]
  [R]_MOSFET = Resistor [tolerance=±5% resistance=100 package="1206 [SMD]"]
  [R]_LED = Resistor [tolerance=±5% resistance=150 package="1206 [SMD]"]
  ANTENNA = LED - 5mm [color="Red (633nm)" package="5 mm [THT]"]
  VIBRATION_MOTOR = LED - 5mm [color="Red (633nm)" package="5 mm [THT]"]

nets:
  N1: AUDIO.RIGHT, AUDIO.LEFT, ATTINY85.Pin_5
  N2: AUDIO.SLEEVE, HEADER_-_POWER.2, RED_LED.cathode, ATTINY85.Pin_4, MOSFET.source, ANTENNA.anode
  N3: HEADER_-_POWER.1, VIBRATION_MOTOR.cathode
  N4: RED_LED.anode, [R]_LED.Pin_0
  N5: ATTINY85.Pin_2, MOSFET.gate, [R]_MOSFET.Pin_0, [R]_MOSFET.Pin_1
  N6: ATTINY85.Pin_3, [R]_LED.Pin_1
  N7: ATTINY85.Pin_7, ANTENNA.cathode
  N8: MOSFET.drain, VIBRATION_MOTOR.anode
