# Fritzing sketch id3935_idee_0 (saved by Fritzing 0.9.3b)
breadboards: 1

parts:
  Onderdeel1 = Arduino Uno (Rev3)
  Onderdeel2 = Bluetooth HC-05 Macho
  R1 = Resistor [tolerance=±5% resistance=220 package=THT]
  LED1 = LED - 5mm [color="Red (633nm)" package="5 mm [THT]"]
  LED2 = LED - 5mm [color="Red (633nm)" package="5 mm [THT]"]

nets:
  N1: Onderdeel1.D12/MISO, LED1.cathode
  N2: Onderdeel1.D13/SCK, LED2.cathode
  N3: Onderdeel1.D0/RX, Onderdeel2.TXD
  N4: Onderdeel1.D1/TX, Onderdeel2.RXD
  5V: Onderdeel1.5V, Onderdeel2.VCC
  GND: Onderdeel1.GND, Onderdeel2.GND, R1.Pin_1
  N5: R1.Pin_0, LED1.anode, LED2.anode
