# Fritzing sketch id3936_circuit_0 (saved by Fritzing 0.9.0b)
breadboards: 1

parts:
  R1 = Resistor [tolerance=±5% resistance=220 package=THT]
  Q1 = NPN-Transistor [part_number=P2N2222A package="TO92 [THT]"]
  M1 = DC Motor
  Part1 = Arduino Uno (Rev3)
  D1 = Rectifier Diode [part_number=1N4001 package="300 mil [THT]"]

nets:
  N1: R1.Pin_0, Part1.D9_PWM
  N2: R1.Pin_1, Q1.B
  N3: Q1.E, M1.pin_2, D1.anode
  N4: Q1.C, Part1.GND
  N5: M1.pin_1, Part1.5V, D1.cathode
