# Fritzing sketch id3937_Spresense_Modulin_0 (saved by Fritzing 0.9.3b)
breadboards: 1

parts:
  M1 = prefix0000
  SparkFun1 = Sen-08680 Soft Potentiometer - 50mm [part_number=SEN-08680]
  R3 = Resistor [tolerance=±5% resistance=2k package=THT]
  R1 = Basic Flex Resistor
  R2 = Resistor [tolerance=±5% resistance=2k package=THT]
  R4 = Trimmer Potentiometer [maximum_resistance=10k package=THT]
  R5 = Trimmer Potentiometer [maximum_resistance=2kΩ package=THT]
  R6 = Trimmer Potentiometer [maximum_resistance=2kΩ package=THT]

nets:
  N1: M1.connector40, R1.pin_1, R4.leg1
  N2: M1.connector41, SparkFun1.connector0, R6.wiper
  N3: M1.connector42, SparkFun1.connector2, R5.wiper
  N4: R3.Pin_0, R1.Pin_2, R2.Pin_0, R4.leg2
  N5: R3.Pin_1, R6.leg2
  N6: R2.Pin_1, R5.leg2
