# Fritzing sketch id3938_SPST_SWITCH_ARDUINO_0 (saved by Fritzing 0.9.2b)
breadboards: 1

parts:
  R1 = Resistor [tolerance=±5% resistance=220 package=THT]
  S1 = Pushbutton [package="[THT]"]
  Part1 = Arduino Uno (Rev3)
  LED1 = LED - 5mm [color="Red (633nm)" package="5 mm [THT]"]

nets:
  N1: R1.Pin_0, LED1.anode
  N2: R1.Pin_1, S1.Pin_1, S1.Pin_2, Part1.5V
  N3: S1.Pin_3, S1.Pin_4
  N4: Part1.GND, LED1.cathode
