# Fritzing sketch id393_335_Servo_0 (saved by Fritzing 0.7.11b)
breadboards: 1

parts:
  Arduino1 = Arduino
  T1 = LM35 Temperature Sensor [package="TO92 [THT]"]  # not connected
  J1 = Basic Servo  # not connected
  LCD1 = LCD screen
  R2 = Resistor [tolerance=±5% resistance=2.2k package=THT]  # not connected
  R3 = Trimmer Potentiometer [maximum_resistance=10kΩ package=THT]  # not connected

nets:
  N1: Arduino1.A4, LCD1.DB7
  N2: Arduino1.A5, LCD1.LED-

notes:
  i2C LCD Shield from adafruit using only 2 pins **not as shown just the screen**
