# Fritzing sketch id3940_Square_Wave_Generator_0 (saved by Fritzing 0.9.3b)
breadboards: 1

parts:
  Componente1 = Arduino Uno (Rev3)
  IC1 = Hex Inverter Schmitt Trigger SN74HC14 [package="DIP (Dual Inline)"]
  R1 = Resistor [tolerance=±5% resistance=100k package=THT]
  C1 = Ceramic Capacitor [capacitance=10nF package="0805 [SMD, multilayer]"]

nets:
  N1: Componente1.A0, IC1.1Y, R1.Pin_1
  5V: Componente1.5V, IC1.VCC
  GND: Componente1.GND, IC1.GND, C1.0
  N2: IC1.1A, R1.Pin_0, C1.1
