# Fritzing sketch id3943_Untitled_Sketch_0 (saved by Fritzing 0.9.0b)
breadboards: 1

parts:
  Part1 = Arduino Ethernet Shield (Rev3)
  R1 = Photocell (LDR) [package=THT]
  R2 = Basic Flex Resistor
  R3 = Basic Flex Resistor
  R4 = Resistor [tolerance=±5% resistance=220 package=THT]
  R5 = Resistor [tolerance=±5% resistance=220 package=THT]
  R6 = Resistor [tolerance=±5% resistance=220 package=THT]

nets:
  N1: Part1.A0, R2.Pin_2, R4.Pin_0
  N2: Part1.A1, R1.pin_1, R5.Pin_0
  N3: Part1.A2, R3.Pin_2, R6.Pin_0
  N4: Part1.5V, R1.pin_0, R2.pin_1, R3.pin_1
  N5: Part1.GND, R4.Pin_1, R5.Pin_1, R6.Pin_1
