# Fritzing sketch id3944_squeezeberry_0 (saved by Fritzing 0.7.12b)
breadboards: 1

parts:
  RaspberryPi1 = Raspberry_Pi_Model_B
  ENCODER1 = Rotary_Encoder_with_Knob
  S1 = Pushbutton [package="[THT]"]
  R1 = Resistor [tolerance=±5% resistance=220 package=THT]
  R2 = Resistor [tolerance=±5% resistance=220 package=THT]
  LCD1 = LCD screen
  R3 = Rotary Potentiometer (Small) [maximum_resistance=100kΩ]

nets:
  N1: RaspberryPi1.connector1, ENCODER1.connector5, S1.Pin_3, S1.Pin_4, LCD1.LED+
  N2: RaspberryPi1.connector2, LCD1.VDD
  N3: RaspberryPi1.connector5, ENCODER1.connector1
  N4: RaspberryPi1.connector6, ENCODER1.connector2, R1.Pin_0, R2.Pin_0, LCD1.VSS, LCD1.R/W, LCD1.LED-, R3.leg2
  N5: RaspberryPi1.connector7, ENCODER1.connector3
  N6: RaspberryPi1.connector11, ENCODER1.connector4, R2.Pin_1
  N7: RaspberryPi1.connector12, LCD1.DB7
  N8: RaspberryPi1.connector15, S1.Pin_1, S1.Pin_2, R1.Pin_1
  N9: RaspberryPi1.connector16, LCD1.DB6
  N10: RaspberryPi1.connector18, LCD1.DB5
  N11: RaspberryPi1.connector22, LCD1.DB4
  N12: RaspberryPi1.connector24, LCD1.E
  N13: RaspberryPi1.connector26, LCD1.RS
  N14: LCD1.V0, R3.wiper
