# Fritzing sketch id3945_Fritzing_test_0 (saved by Fritzing 0.9.1b)
breadboards: 1

parts:
  Part1 = Triple Axis Accelerometer Breakout - ADXL335
  Raspberry_Pi1 = Raspberry Pi B+

nets:
  N1: Part1.ZOUT, Raspberry_Pi1.GPIO25
  N2: Part1.YOUT, Raspberry_Pi1.GND
  N3: Part1.XOUT, Raspberry_Pi1.GPIO24
