# Fritzing sketch id3946_SSA_0 (saved by Fritzing 0.9.1b)
breadboards: 1

parts:
  Part1 = Arduino Uno (Rev3)
  J1 = Piezo Speaker
  Part2 = Bluetooth Mate Silver
  T1 = TMP36 Temperature Sensor [package="TO92 [THT]"]
  J2 = Basic Force Sensing Resistor (FSR) [package=THT]
  R1 = Resistor [tolerance=±5% resistance=10k package=THT]
  Part3 = USB LiPoly Charger
  U1 = LIPO-1000mAh [package=lipo-1000]
  LED1 = LED - 3mm [color="Red (633nm)" package="3 mm [THT]"]
  R2 = TRIMPOT [package=trimpot_pth_s3_lock]
  R3 = Resistor [tolerance=±5% resistance=1k package="0805 [SMD]"]

nets:
  N1: Part1.A0, J2.pin_0, R1.Pin_1
  N2: Part1.A1, T1.Vout
  N3: Part1.A2, R2.WIPER
  N4: Part1.D8, LED1.cathode, R3.Pin_1
  N5: Part1.D13/SCK, J1.pin2
  GND: Part1.GND, J1.pin1, Part2.GND, T1.GND, R1.Pin_0, Part3.GND, U1.-, LED1.anode, R2.CCW
  N6: Part1.D0/RX, Part2.TX_5V
  N7: Part1.D1/TX, Part2.RX_5V
  5V: Part1.5V, Part2.VCC, T1.+Vs, J2.pin_1, R2.CW, R3.Pin_0
  N8: Part1.VIN, Part3.VBAT, U1.+
