# Fritzing sketch id3947_SSS_Project_0 (saved by Fritzing 0.9.2b)
breadboards: 1

parts:
  VCC1 = Battery
  J1 = Piezo Speaker
  Part1 = Arduino Due (Rev2b)
  M1 = DC Motor
  U1 = TMP36 [package=to-92]
  S1 = Pushbutton [package="[THT]"]
  S2 = Pushbutton [package="[THT]"]
  S3 = Pushbutton [package="[THT]"]
  S4 = Pushbutton [package="[THT]"]

nets:
  GND: VCC1.-, J1.pin1, Part1.GND, M1.pin_2, U1.GND
  VIN: VCC1.+, Part1.VIN, Part1.D49, U1.VCC, S4.Pin_3, S4.Pin_4
  N1: J1.pin2, Part1.D26
  N2: Part1.A0, U1.VOUT
  N3: Part1.D25, M1.pin_1
  N4: Part1.D43, S1.Pin_3, S1.Pin_4
  N5: Part1.D45, S2.Pin_3, S2.Pin_4
  N6: Part1.D47, S3.Pin_3, S3.Pin_4
