# Fritzing sketch id3949_stacja2.0_0 (saved by Fritzing 0.9.3b)
breadboards: 1

parts:
  Part1 = Arduino Nano (Rev3.0)
  Part2 = bme680
  U1 = Nokia 6100 Color LCD [package=nokia6100_lcd]  # not connected
  R3 = Resistor [tolerance=±5% resistance=4.7k package=THT]
  R4 = Resistor [tolerance=±5% resistance=4.7k package=THT]

nets:
  N1: Part1.A5, Part1.A4, R3.Pin_0, R4.Pin_0
  N2: Part2.connector8, R3.Pin_1
  N3: Part2.connector9, R4.Pin_1

notes:
  1 - VCC
  2 - GND
  3 - AOUT
  4 - ILED
  Czujnik GP2Y1010AU0F
  1  2  3  4
  Rst CE DC DIN CLK VCC BL GND
  Nokia 5110
