# Fritzing sketch id3951_Lights_0 (saved by Fritzing 0.9.1b)
breadboards: 1

parts:
  Part1 = Arduino Uno (Rev3)
  JP1 = Header 4 [package=1x04-smd]
  Q2 = Basic FET N-Channel [package="D2Pak [SMD]"]
  R1 = Resistor [package="0402 [SMD]"]
  Q3 = Basic FET N-Channel [package="D2Pak [SMD]"]
  Q4 = Basic FET N-Channel [package="D2Pak [SMD]"]
  R2 = Resistor [package="0402 [SMD]"]
  Part2 = Lilypad Power Supply
  R3 = Resistor [package="0402 [SMD]"]
  S1 = Pushbutton [package="[SMD]"]  # not connected
  R4 = Resistor [package="0402 [SMD]"]

nets:
  GND: Part1.GND, Q2.source, R1.Pin_0, Q3.source, Q4.source, R2.Pin_0, Part2.GND, R3.Pin_0, R4.Pin_0
  N1: Part1.D3_PWM, Q4.Gate
  N2: Part1.D5_PWM, Q3.Gate
  N3: Part1.D6_PWM, Q2.Gate
  N4: JP1.1, Q2.drain, R1.Pin_1
  N5: JP1.2, Q4.drain, R3.Pin_1
  N6: JP1.3, Q3.drain, R2.Pin_1
  N7: JP1.4, Part2.+
