# Fritzing sketch id3954_Untitled_Sketch_0 (saved by Fritzing 0.9.0b)
breadboards: 1

parts:
  Часть1 = Arduino Uno (Rev3) [part_number=1]
  R1 = Resistor [tolerance=±5% resistance=10 package="0805 [SMD]"]
  Thermistor_10K = Resistor [tolerance=±5% resistance=10 package=THT]
  Relay = Relay [part_number=FRS1B-S package=THT]
  Heat = Peltier Element [part_number=TEC-]

nets:
  N1: Часть1.A1, R1.Pin_1
  N2: Часть1.D8, Relay.COIL2
  N3: Часть1.5V, Thermistor_10K.Pin_0
  N4: Часть1.GND, Relay.COIL1, Heat.pin1
  N5: R1.Pin_0, Thermistor_10K.Pin_1
  N6: Relay.C1, Relay.C2, Heat.pin2
