# Fritzing sketch id3955_Untitled_Sketch_Go3BTS8_0 (saved by Fritzing 0.9.0b)
circuit board: 3.58098cm x 3.21957cm
breadboards: 1

parts:
  Часть1 = Arduino Uno (Rev3) [part_number=1]
  Thermistor_10K = Resistor [tolerance=±5% resistance=10 package=THT]
  Relay = Relay [part_number=FRS1B-S package=THT]
  Heat = Peltier Element [part_number=TEC-]
  JP1 = Header 1 [package=smtso-256-et]
  R1 = Resistor [tolerance=±5% resistance=10 package=THT]
  JP4 = Header 1 [package=smtso-256-et]
  JP5 = Header 1 [package=smtso-256-et]
  JP6 = Header 1 [package=smtso-256-et]

nets:
  N1: Часть1.A1, R1.Pin_1, JP5.1
  N2: Часть1.D8, Relay.COIL2, JP4.1
  N3: Часть1.GND, Relay.COIL1, Heat.pin1, JP1.1
  N4: Часть1.5V, Thermistor_10K.Pin_0
  N5: Thermistor_10K.Pin_1, R1.Pin_0, JP6.1
  N6: Relay.C1, Relay.C2, Heat.pin2
