# Fritzing sketch id3956_Standalone_328_lcd_0 (saved by Fritzing 0.9.3b)
circuit board: 11cm x 9cm
breadboards: 1

parts:
  AREF_A0-5 = male pin header, 7 pins [form="♂ (male)"]
  5v_in = male pin header, 1 pin [form="♂ (male)"]
  -_+ = male pin header, 1 pin [form="♂ (male)"]
  16MHz = Crystal [frequency="16 Mhz" package=THT]
  C3 = Capacitor [package=cap-pth-small2]
  C4 = Capacitor [package=cap-pth-small2]
  R1 = Resistor [tolerance=±5% resistance=220 package=THT]
  R2 = Resistor [tolerance=±5% resistance=220 package=THT]
  LED13 = LED - 5mm [color="Red (633nm)" package="5 mm [THT]"]
  Reset = Momentary Switch [package=ksa_sealed_tac_switch]
  5v = male pin header, 4 pins [form="♂ (male)"]
  GND = male pin header, 4 pins [form="♂ (male)"]
  L7805 = Voltage Regulator - 3.3V [package="TO220 [THT]"]
  C1 = Capacitor Polarized [package=cpol-radial-10uf-25v]
  C2 = Capacitor Polarized [package=cpol-radial-10uf-25v]
  R3 = TRIMPOT [package=trimpot-5mm]
  C6 = Capacitor Polarized [package=cpol-radial-10uf-25v]
  ATmega = atmega328 [package=dip]
  J3 = male pin header, 1 pin [form="♂ (male)"]
  J4 = male pin header, 1 pin [form="♂ (male)"]
  U3 = LCD-16X2 [package=lcd-16x2]
  part = male pin header, 4 pins [form="♂ (male)"]
  part_2 = male pin header, 1 pin [form="♂ (male)"]
  part_3 = male pin header, 1 pin [form="♂ (male)"]
  C7 = Capacitor [package=cap-pth-small2]
  D1 = Diode [package=diode-1n4001]
  D2 = Diode [package=diode-1n4001]
  J6 = male pin header, 1 pin [form="♂ (male)"]
  J7 = Screw terminal - 2 pins [package=THT]
  TRANSFORMER = Screw terminal - 2 pins [package=THT]
  IC2 = Voltage Regulator LM1117 [package=sot223]
  J9 = male pin header, 1 pin [form="♂ (male)"]
  ESP_01 = female pin header, 4 pins [form="♀ (female)"]
  part_4 = female pin header, 4 pins [form="♀ (female)"]
  J12 = male pin header, 1 pin [form="♂ (male)"]

nets:
  N1: AREF_A0-5.pin1, ATmega.A5
  N2: AREF_A0-5.pin2, ATmega.A4
  N3: AREF_A0-5.pin3, ATmega.A3
  N4: AREF_A0-5.pin4, ATmega.A2
  N5: AREF_A0-5.pin5, ATmega.A1
  N6: AREF_A0-5.pin6, ATmega.A0
  N7: AREF_A0-5.pin7, ATmega.AREF
  N8: 5v_in.pin1, R1.Pin_1, R2.Pin_0, 5v.pin1, 5v.pin2, 5v.pin3, 5v.pin4, L7805.output_voltage, C2.+, ATmega.VCC, ATmega.AVCC, U3.DB5
  GND: -_+.pin1, C3.2, C4.1, Reset.4, R3.CCW, ATmega.GND, U3.VSS, U3.K, part_3.pin1, IC2.IN, ESP_01.pin1
  N9: 16MHz.pin_0, C3.1, ATmega.XLAT1
  N10: 16MHz.pin_1, C4.2, ATmega.XLAT2
  N11: R1.Pin_0, Reset.1, ATmega.RESET
  N12: R2.Pin_1, LED13.anode
  N13: LED13.cathode, ATmega.D13
  N14: GND.pin1, GND.pin2, GND.pin3, GND.pin4, L7805.GND, C1.-, C2.-, C6.-, J6.pin1, TRANSFORMER.pin1
  N15: L7805.input_voltage, C1.+, C6.+, D1.C, D2.C
  N16: R3.CW, U3.VDD, U3.R_W, U3.A
  N17: ATmega.D0_(RX), part.pin2
  N18: ATmega.D2, U3.RS
  N19: ATmega.D3_(PWM), U3.E
  N20: ATmega.D4, U3.DB4
  N21: ATmega.D5_(PWM), U3.DB6
  N22: ATmega.D6_(PWM), U3.DB7
  N23: ATmega.D7, part_4.pin1, part_4.pin2
  N24: ATmega.D8, ESP_01.pin4
  N25: ATmega.D9_(PWM), J12.pin1
  N26: ATmega.D10_(PWM), J4.pin1
  N27: ATmega.D11_(PWM), J9.pin1
  N28: ATmega.D12, J3.pin1
  N29: part_2.pin1, C7.2
  N30: D1.A, TRANSFORMER.pin2
  N31: D2.A, J7.pin2
  N32: IC2.OUT, part_4.pin4

notes:
  7.5-25v
  MKCE EEE
  Power Monitor
  + - Tx Rx
  + -
  9-0-9
