# Fritzing sketch id3957_standalone_328_with_7805_v7_anon_0 (saved by Fritzing 0.9.0b)
breadboards: 1

parts:
  R1 = Resistor [tolerance=±5% resistance=10k package=THT]
  C1 = Ceramic Capacitor [capacitance=22pF package="100 mil [THT, multilayer]"]
  Xtal1 = CRYSTAL - kHz [frequency="16 Mhz"]
  C2 = Ceramic Capacitor [capacitance=22pF package="100 mil [THT, multilayer]"]
  R2 = Resistor [tolerance=±5% resistance=560 package=THT]
  LED1 = LED - 5mm [color="Red (633nm)" package="5 mm [THT]"]
  J1 = Screw terminal - 2 pins [package=THT]
  D1 = Rectifier Diode [part_number=1N5059 package="300 mil [THT]"]
  D2 = Rectifier Diode [part_number=1N5059 package="300 mil [THT]"]
  D3 = Rectifier Diode [part_number=1N5059 package="300 mil [THT]"]
  D4 = Rectifier Diode [part_number=1N5059 package="300 mil [THT]"]
  C3 = Electrolytic Capacitor [capacitance=1mF package="100 mil [THT, electrolytic]"]
  C4 = Ceramic Capacitor [capacitance=100nF package="100 mil [THT, multilayer]"]
  D5 = Rectifier Diode [part_number=1N4001 package="300 mil [THT]"]
  C5 = Electrolytic Capacitor [capacitance=1µF package="100 mil [THT, electrolytic]"]
  C6 = Ceramic Capacitor [capacitance=100nF package="100 mil [THT, multilayer]"]
  LED2 = LED - 5mm [color="Green (565nm)" package="5 mm [THT]"]
  R3 = Resistor [tolerance=±5% resistance=470 package=THT]
  IC2 = voidyourwarranty
  IC1 = voidyourwarranty

nets:
  N1: R1.Pin_0, LED1.anode, D5.anode, C5.+, C6.0, LED2.anode, IC2.connector2, IC1.connector6, IC1.connector19
  N2: R1.Pin_1, IC1.connector0
  N3: C1.0, C2.1, D3.anode, D4.anode, C3.-, C4.1, C5.-, C6.1, R3.Pin_1, IC2.connector0, IC1.connector7, IC1.connector21
  N4: C1.1, Xtal1.pin_1, IC1.connector8
  N5: Xtal1.pin_0, C2.0, IC1.connector9
  N6: R2.Pin_0, IC1.connector18
  N7: R2.Pin_1, LED1.cathode
  N8: J1.pin1, D2.anode, D4.cathode
  N9: J1.pin2, D1.anode, D3.cathode
  N10: D1.cathode, D2.cathode, C3.+, C4.0, D5.cathode, IC2.connector1
  N11: LED2.cathode, R3.Pin_0
