# Fritzing sketch id3959_tono_star_wars_0 (saved by Fritzing 0.9.3b)
breadboards: 1

parts:
  Componente1 = Arduino Uno (Rev3)
  R1 = Resistor [tolerance=±5% resistance=220 package=THT]
  R2 = Resistor [tolerance=±5% resistance=220 package=THT]
  LED1 = LED - 5mm [color="Red (633nm)" package="5 mm [THT]"]
  LED2 = LED - 5mm [color="Red (633nm)" package="5 mm [THT]"]
  J1 = Piezo Speaker

nets:
  N1: Componente1.D9_PWM, J1.pin1
  N2: Componente1.D4, LED1.anode
  N3: Componente1.D6_PWM, LED2.anode
  N4: R1.Pin_0, R2.Pin_0, J1.pin2
  N5: R1.Pin_1, LED1.cathode
  N6: R2.Pin_1, LED2.cathode
