# Fritzing sketch id3960_StartLCD_0 (saved by Fritzing 0.9.2b)
breadboards: 1

parts:
  LCD1 = LCD screen
  R1 = Rotary Potentiometer (Small) [maximum_resistance=100kΩ package=THT]
  Raspberry_Pi1 = Raspberry Pi B+

nets:
  VSS: LCD1.VSS, R1.leg2, Raspberry_Pi1.GND
  VDD: LCD1.VDD, R1.leg1, Raspberry_Pi1.5V
  N1: LCD1.V0, R1.wiper
  N2: LCD1.RS, Raspberry_Pi1.GPIO22
  N3: LCD1.R/W, Raspberry_Pi1.GPIO24
  N4: LCD1.E, Raspberry_Pi1.GPIO23
  N5: LCD1.DB4, Raspberry_Pi1.GPIO9
  N6: LCD1.DB5, Raspberry_Pi1.GPIO25
  N7: LCD1.DB6, Raspberry_Pi1.GPIO11
  N8: LCD1.DB7, Raspberry_Pi1.GPIO8

notes:
  Pin LCD = PIN GPIO
  1 = GND
  2 = 5V
  4 = GPIO 22
  5 = GPIO 23
  6 = GPIO 24
  11 = GPIO 9
  12 = GPIO 25
  13 = GPIO 11
  14 = GPIO
