# Fritzing sketch id3961_depart_course_led_0 (saved by Fritzing 0.9.3b)
breadboards: 1

parts:
  Composant1 = Arduino Uno (Rev3)
  LED1 = LED - 5mm [color="Red (633nm)" package="5 mm [THT]"]
  LED2 = LED - 5mm [color="Red (633nm)" package="5 mm [THT]"]
  S1 = Pushbutton [package="[THT]"]
  J1 = Piezo Speaker
  R1 = Resistor [tolerance=±5% resistance=220 package=THT]
  R2 = Resistor [tolerance=±5% resistance=1M package=THT]
  R3 = Resistor [tolerance=±5% resistance=10k package=THT]
  R4 = Resistor [tolerance=±5% resistance=220 package=THT]
  R5 = Resistor [tolerance=±5% resistance=220 package=THT]
  LED3 = LED - 5mm [color="Green (565nm)" package="5 mm [THT]"]

nets:
  N1: Composant1.D2, S1.Pin_3, S1.Pin_4, R3.Pin_1
  N2: Composant1.D3_PWM, LED1.anode
  N3: Composant1.D4, LED2.anode
  N4: Composant1.D5_PWM, LED3.anode
  N5: Composant1.D6_PWM, J1.pin1, R2.Pin_1
  N6: Composant1.5V, S1.Pin_1, S1.Pin_2, J1.pin2
  N7: Composant1.GND, R1.Pin_0, R2.Pin_0, R3.Pin_0, R4.Pin_0, R5.Pin_0
  N8: LED1.cathode, R5.Pin_1
  N9: LED2.cathode, R4.Pin_1
  N10: R1.Pin_1, LED3.cathode
