# Fritzing sketch id3962_carrera_decode_mit_Neopixel_0 (saved by Fritzing 0.9.3b)
breadboards: 1

parts:
  R1 = Resistor [tolerance=±5% resistance=22k package=THT]
  D1 = Rectifier Diode [part_number=1N4001 package="300 mil [THT]"]
  R2 = Resistor [tolerance=±5% resistance=8.2k package=THT]
  Bauteil1 = Arduino Nano (Rev3.0)
  NEOPIXEL2 = adafruit [part_number=1461]
  LM1 = RioRand LM2596
  Carrera_Controll_Unit_1 = Carrera_Controll_Unit_30352 [part_number=20030352]
  D2 = Rectifier Diode [part_number=1N4001 package="300 mil [THT]"]
  D3 = Rectifier Diode [part_number=1N4001 package="300 mil [THT]"]

nets (from the breadboard view):
  N1: R1.Pin_0, D1.cathode
  N2: R1.Pin_1, R2.Pin_0, Bauteil1.D2
  N3: D1.anode, Carrera_Controll_Unit_1.connector2, D2.anode
  N4: R2.Pin_1, Bauteil1.RESET, Bauteil1.GND, NEOPIXEL2.connector3, LM1.Pin_3, Carrera_Controll_Unit_1.connector7
  N5: Bauteil1.D6, Bauteil1.D7, NEOPIXEL2.connector2
  N6: Bauteil1.VIN, D3.cathode
  N7: NEOPIXEL2.connector1, LM1.Pin_2, D3.anode
