# Fritzing sketch id3963_Stepper_Box_0 (saved by Fritzing 0.9.3b)
breadboards: 2

parts:
  Part1 = Arduino Uno (Rev3)
  Part2 = EasyDriver_v44
  Part3 = EasyDriver_v44
  S1 = Momentary Switch [package=ksa_sealed_tac_switch]
  M1 = Stepper Motor - Bipolar
  M2 = Stepper Motor - Bipolar
  S3 = Momentary Switch [package=ksa_sealed_tac_switch]
  BAT1 = BC9VPC [package=bc9vpc]
  R1 = Resistor [tolerance=±5% resistance=220 package="2010 [SMD]"]
  R2 = Resistor [tolerance=±5% resistance=220 package="2010 [SMD]"]

nets:
  N1: Part1.D8, Part2.DIR
  N2: Part1.D9_PWM, Part2.STEP
  GND: Part1.GND, Part2.GND, Part2.V+, Part3.GND, Part3.V+, S1.3, S3.2, BAT1.V+, BAT1.V-
  N3: Part1.D2, S1.1, R1.Pin_0
  N4: Part1.D3_PWM, S3.4, R2.Pin_0
  N5: Part1.D6_PWM, Part3.DIR
  N6: Part1.D7, Part3.STEP
  N7: Part1.3V3, R1.Pin_1, R2.Pin_1
  N8: Part2.OUT2B, M2.A
  N9: Part2.OUT1A, M2.C
  N10: Part2.OUT1B, M2.B
  N11: Part3.OUT2A, M1.A
  N12: Part3.OUT2B, M1.C
  N13: Part3.OUT1A, M1.B
  N14: Part3.OUT1B, M1.D

notes:
  Up
  Down
