# Fritzing sketch id3964_stepper_motor_devre_0 (saved by Fritzing 0.9.3b)
breadboards: 1

parts:
  MOTOR2 = 28BYJ-48
  X1 = X113647
  MOTOR1 = 28BYJ-48
  X2 = X113647
  Parça1 = Arduino Uno (Rev3)

nets:
  N1: MOTOR2.connector1, X2.connector7
  N2: MOTOR2.connector2, X2.connector8
  N3: MOTOR2.connector3, X2.connector11
  N4: MOTOR2.connector4, X2.connector10
  N5: MOTOR2.connector5, X2.connector9
  N6: X1.connector1, Parça1.D8
  N7: X1.connector2, Parça1.D9_PWM
  N8: X1.connector3, Parça1.D10_PWM/SS
  N9: X1.connector4, Parça1.D11_PWM/MOSI
  N10: X1.connector5, X2.connector5, Parça1.GND
  N11: X1.connector6, X2.connector6, Parça1.5V
  N12: X1.connector7, MOTOR1.connector1
  N13: X1.connector8, MOTOR1.connector2
  N14: X1.connector9, MOTOR1.connector5
  N15: X1.connector10, MOTOR1.connector4
  N16: X1.connector11, MOTOR1.connector3
  N17: X2.connector1, Parça1.D2
  N18: X2.connector2, Parça1.D3_PWM
  N19: X2.connector3, Parça1.D5_PWM
  N20: X2.connector4, Parça1.D6_PWM

notes:
  sol motor (ilk baglantı)
  Stepper Motor Devresi
