# Fritzing sketch id3965_20_Stepper_Motor_Control_Fritzing_0 (saved by Fritzing 0.8.7b)
breadboards: 1

parts:
  IC1 = ULN2003A [package="DIP16 [THT]"]
  U1 = Voltage Regulator - 5V [package="TO220 [THT]"]
  Part1 = Arduino Uno (Rev3)
  M2 = Stepper Motor - Unipolar

nets:
  N1: IC1.In_1, Part1.D3_PWM
  N2: IC1.In_2, Part1.D5_PWM
  N3: IC1.In_3, Part1.D6_PWM
  N4: IC1.In_4, Part1.D9_PWM
  GND: IC1.0V, U1.GND, Part1.GND
  N5: IC1.COM_-_Common, Part1.5V
  N6: IC1.Out_4, M2.D
  N7: IC1.Out_3, M2.B
  N8: IC1.Out_2, M2.C
  N9: IC1.Out_1, M2.A
  N10: U1.input_voltage, Part1.VIN
  N11: U1.output_voltage, M2.COMMON_1, M2.COMMON_2
