# Fritzing sketch id3966_Stepper_motor_control_for_4th_cnc_shaft_0 (saved by Fritzing 0.9.3b)
perfboards: 1

parts:
  uC2 = generic_sip_50_300mil.fzp
  R4 = Resistor [tolerance=±5% resistance=10k package=THT]
  3v3_+_- = female pin header, 2 pins [form="♀ (female)"]
  R6 = Resistor [tolerance=±5% resistance=10k package=THT]
  C4 = Ceramic Capacitor [capacitance=10nF package="100 mil [THT, multilayer]"]
  R8 = Resistor [tolerance=±5% resistance=10k package=THT]
  Select = Pushbutton [package="[THT]"]
  R5 = Resistor [tolerance=±5% resistance=330 package=THT]
  R7 = Resistor [tolerance=±5% resistance=330 package=THT]
  C3 = Ceramic Capacitor [capacitance=10nF package="100 mil [THT, multilayer]"]
  Enable = Pushbutton [package="[THT]"]
  Reset = Pushbutton [package="[THT]"]
  Up = Pushbutton [package="[THT]"]
  C2 = Ceramic Capacitor [capacitance=10nF package="100 mil [THT, multilayer]"]
  MD09B1 = A4988 Stepper Motor Driver Carrier
  R2 = Resistor [tolerance=±5% resistance=10k package=THT]
  C1 = Ceramic Capacitor [capacitance=10nF package="100 mil [THT, multilayer]"]
  R3 = Resistor [tolerance=±5% resistance=330 package=THT]
  R9 = Resistor [tolerance=±5% resistance=330 package=THT]
  Reset_2 = male pin header, 1 pin [form="♂ (male)"]
  5-_Up = male pin header, 1 pin [form="♂ (male)"]
  6_-_Enable = male pin header, 1 pin [form="♂ (male)"]
  4_-_Select = male pin header, 1 pin [form="♂ (male)"]
  C5 = Electrolytic Capacitor [capacitance=10µF voltage=50V package="1010 [SMD, electrolytic]"]
  C7 = Ceramic Capacitor [capacitance=10nF package="100 mil [THT, multilayer]"]
  R13 = Resistor [tolerance=±5% resistance=10k package=THT]
  R14 = Resistor [tolerance=±5% resistance=330 package=THT]
  3V3-microswitch = male pin header, 1 pin [form="♂ (male)"]
  NO-microswitch = male pin header, 1 pin [form="♂ (male)"]
  FCP = male pin header, 1 pin [form="♂ (male)"]
  R15 = Resistor [tolerance=±5% resistance=330 package=THT]
  R16 = Resistor [tolerance=±5% resistance=10k package=THT]
  Anodo_Led = male pin header, 1 pin [form="♂ (male)"]
  Col_Trans = male pin header, 1 pin [form="♂ (male)"]
  GND = male pin header, 1 pin [form="♂ (male)"]
  S2 = Limit Switch SPDT
  M2 = prefix0000
  U1 = prefix0000

nets:
  N1: uC2.connector2, R14.Pin_0, FCP.pin1
  N2: uC2.connector4, R5.Pin_0, 4_-_Select.pin1
  N3: uC2.connector5, R7.Pin_0, 5-_Up.pin1
  N4: uC2.connector6, R9.Pin_0, 6_-_Enable.pin1
  N5: uC2.connector11, MD09B1.STEP
  N6: uC2.connector12, MD09B1.DIR, MD09B1.OUT_1A, M2.connector0
  N7: uC2.connector45, R4.Pin_0, 3v3_+_-.pin2, R6.Pin_0, C4.0, R8.Pin_0, C3.0, C2.0, R2.Pin_0, C1.0, C7.0, R13.Pin_0, GND.pin1, U1.connector1, U1.connector3
  N8: uC2.connector47, MD09B1.Enable, MD09B1.GROUND, C5.-
  N9: uC2.connector48, 3v3_+_-.pin1, Select.Pin_1, Select.Pin_2, Enable.Pin_1, Enable.Pin_2, Reset.Pin_1, Reset.Pin_2, Up.Pin_1, Up.Pin_2, MD09B1.VDD, C5.+, 3V3-microswitch.pin1, R15.Pin_0, R16.Pin_1, S2.connector1
  N10: R4.Pin_1, Select.Pin_3, Select.Pin_4, R5.Pin_1, C2.1
  N11: R6.Pin_1, R7.Pin_1, C3.1, Up.Pin_3, Up.Pin_4
  N12: C4.1, R8.Pin_1, Enable.Pin_3, Enable.Pin_4, R9.Pin_1
  N13: Reset.Pin_3, Reset.Pin_4, R2.Pin_1, C1.1, R3.Pin_1
  N14: MD09B1.MS2, MD09B1.VMOT
  N15: MD09B1.RESET, MD09B1.SLEEP
  N16: MD09B1.OUT_2B, M2.connector3
  N17: MD09B1.OUT_2A, M2.connector2
  N18: MD09B1.OUT_1B, M2.connector1
  N19: R3.Pin_0, Reset_2.pin1
  N20: C7.1, R13.Pin_1, R14.Pin_1, NO-microswitch.pin1, S2.connector2
  N21: R15.Pin_1, Anodo_Led.pin1, U1.connector0
  N22: R16.Pin_0, Col_Trans.pin1, U1.connector2

notes:
  Reset
  Select
  Up
  Enable
