# Fritzing sketch id3967_l298n_stepper_arduino_0 (saved by Fritzing 0.9.0b)

parts:
  M2 = Stepper Motor - Bipolar
  U1 = L298 [package=multiwatt15]
  U2 = LIPO-1000mAh [package=lipo-1000]
  Part2 = Arduino Uno (Rev3) - ICSP

nets:
  N1: M2.A, U1.OUT1
  N2: M2.C, U1.OUT2
  N3: M2.B, U1.OUT3
  N4: M2.D, U1.OUT4
  N5: U1.VS, U2.+
  N6: U1.IN1, Part2.D13/SCK
  N7: U1.ENA, U1.ENB
  N8: U1.IN2, Part2.D12/MISO
  GND: U1.GND, U2.-, Part2.GND
  N9: U1.IN3, Part2.D11_PWM/MOSI
  N10: U1.IN4, Part2.D10_PWM/SS
