# Fritzing sketch id3969_My_sketch_0 (saved by Fritzing 0.9.2b)
circuit board: 11cm x 6.95cm
breadboards: 1

parts:
  EasyDriver_RHS = EasyDriver_v44
  R2 = Resistor [tolerance=±5% resistance=220 package=THT]  # not connected
  J5 = Screw terminal - 2 pins [package=THT]
  R3 = Resistor [tolerance=±5% resistance=220 package=THT]  # not connected
  R4 = Resistor [tolerance=±5% resistance=220 package=THT]  # not connected
  Arduino = Arduino Nano (Rev3.0)
  R1 = Resistor [tolerance=±5% resistance=100 package=THT]  # not connected
  M1 = Stepper Motor - Bipolar
  EasyDriver_LHS = EasyDriver_v44
  M2 = Stepper Motor - Bipolar
  J7 = shrouded pin header, 20 pins [form="♂ (shrouded male)"]
  U3 = mystery part, 1 pin [chip_label=?]  # not connected
  U4 = mystery part, 1 pin [chip_label=?]  # not connected
  U5 = mystery part, 1 pin [chip_label=?]  # not connected
  U6 = mystery part, 1 pin [chip_label=?]  # not connected
  S1 = Toggle Switch [package=THT]  # not connected

nets:
  GND: EasyDriver_RHS.GND, J5.pin1, Arduino.GND
  N1: EasyDriver_RHS.V+, J5.pin2
  N2: EasyDriver_RHS.STEP, Arduino.D8, EasyDriver_LHS.STEP
  N3: EasyDriver_RHS.DIR, Arduino.D9, EasyDriver_LHS.DIR
  N4: EasyDriver_RHS.OUT2A, M1.A
  N5: EasyDriver_RHS.OUT2B, M1.C
  N6: EasyDriver_RHS.OUT1A, M1.B
  N7: EasyDriver_RHS.OUT1B, M1.D
  N8: Arduino.D2, J7.pin11
  N9: Arduino.D3, J7.pin10
  N10: Arduino.D7, EasyDriver_LHS.GND
  N11: EasyDriver_LHS.OUT2A, M2.A
  N12: EasyDriver_LHS.OUT2B, M2.C
  N13: EasyDriver_LHS.OUT1A, M2.B
  N14: EasyDriver_LHS.OUT1B, M2.D

notes:
  sw_lft_up
  Voltage
  Regulator
