# Fritzing sketch id396_ds18b20_0 (saved by Fritzing 0.7.9b)
breadboards: 1

parts:
  Arduino1 = Arduino
  part = TMP36 Temperature Sensor [package="TO92 [THT]"]  # not connected
  T1 = TMP36 Temperature Sensor [package="TO92 [THT]"]
  R1 = Resistor [tolerance=±5% resistance=4.7k package=THT]

nets:
  N1: Arduino1.D10, T1.Vout, R1.Pin_1
  N2: Arduino1.+5V, R1.Pin_0
  N3: Arduino1.GND, T1.+Vs
