# Fritzing sketch id3970_slot_machine_steppers_0 (saved by Fritzing 0.9.1b)

parts:
  Composant1 = Arduino Mega ADK (Rev3)
  M2 = Stepper Motor - Unipolar
  M3 = Stepper Motor - Unipolar
  IC1 = ULN2003A [package="DIP16 [THT]"]
  IC2 = ULN2003A [package="DIP16 [THT]"]
  IC3 = ULN2003A [package="DIP16 [THT]"]
  VCC1 = 4 x AAA Battery Mount
  M4 = Stepper Motor - Unipolar
  S1 = Pushbutton [package="[THT]"]

nets:
  N1: Composant1.D13_PWM, IC1.In_1
  N2: Composant1.D12_PWM, IC1.In_2
  N3: Composant1.D11_PWM, IC1.In_3
  N4: Composant1.D10_PWM, IC1.In_4
  N5: Composant1.D9_PWM, IC2.In_1
  N6: Composant1.D8_PWM, IC2.In_2
  N7: Composant1.5V, S1.Pin_3
  N8: Composant1.D2_PWM, IC3.In_4
  N9: Composant1.D3_PWM, IC3.In_3
  N10: Composant1.D4_PWM, IC3.In_2
  N11: Composant1.D5_PWM, IC3.In_1
  N12: Composant1.D6_PWM, IC2.In_4
  N13: Composant1.D7_PWM, IC2.In_3
  N14: Composant1.D49, S1.Pin_1, S1.Pin_2
  N15: M2.A, IC2.Out_1
  N16: M2.COMMON_1, M2.COMMON_2, IC2.COM_-_Common
  N17: M2.C, IC2.Out_3
  N18: M2.B, IC2.Out_2
  N19: M2.D, IC2.Out_4
  N20: M3.A, IC3.Out_1
  N21: M3.COMMON_1, M3.COMMON_2, IC3.COM_-_Common
  N22: M3.C, IC3.Out_3
  N23: M3.B, IC3.Out_2
  N24: M3.D, IC3.Out_4
  N25: IC1.COM_-_Common, VCC1.+, M4.COMMON_1, M4.COMMON_2
  N26: IC1.Out_4, M4.D
  N27: IC1.Out_3, M4.C
  N28: IC1.Out_2, M4.B
  N29: IC1.Out_1, M4.A
  N30: IC2.In_6, IC2.In_7, IC2.0V
