# Fritzing sketch id3971_arduino_p_lcd_p_stepper_p_buttons_0 (saved by Fritzing 0.8.3b)
breadboards: 1

parts:
  Onderdeel1 = Arduino Uno (Rev3)
  Onderdeel2 = 2A_MOTOR_SHIELD_9
  LCD1 = LCD screen
  R1 = Rotary Potentiometer (Small)
  M1 = Stepper Motor - Bipolar
  left = Pushbutton [package="[THT]"]
  speed_up = Pushbutton [package="[THT]"]
  speed_down = Pushbutton [package="[THT]"]
  right = Pushbutton [package="[THT]"]

nets:
  N1: Onderdeel1.A0, Onderdeel2.connector1pad-4-5-0-3-1-5-3-7
  N2: Onderdeel1.A1, Onderdeel2.connector1pad-0-1-9-9-4-6-9
  N3: Onderdeel1.A2, Onderdeel2.connector1pad-4-2-3-6-2-3-6
  N4: Onderdeel1.A3, Onderdeel2.connector1pad-4-5-0-39-8-14-4
  N5: Onderdeel1.A4/SDA, Onderdeel2.connector1pad-0-1-1-48-61-0
  N6: Onderdeel1.A5/SCL, Onderdeel2.connector1pad-4-2-34-9-8-1
  GND: Onderdeel1.GND, Onderdeel2.connector1pad-0-1-1-48-61, Onderdeel2.connector1pad-0-1-9-9-4-9, Onderdeel2.connector1pad-4-5-0-39-8-14, LCD1.VSS, LCD1.RS, R1.leg1
  N7: Onderdeel1.D8, Onderdeel2.connector1pad-4-5-9-4-3, M1.C
  N8: Onderdeel1.D9_PWM, Onderdeel2.connector1pad-47-4-0-0, M1.A
  N9: Onderdeel1.D10_PWM/SS, Onderdeel2.connector1pad-4-2-34-9-7
  N10: Onderdeel1.D11_PWM/MOSI, Onderdeel2.connector1pad-0-1-1-48-6, LCD1.DB0
  N11: Onderdeel1.D12/MISO, Onderdeel2.connector1pad-4-5-0-39-8-1, LCD1.R/W
  N12: Onderdeel1.D13/SCK, Onderdeel2.connector1pad-4-2-3-6-2-1
  N13: Onderdeel1.AREF, Onderdeel2.connector1pad-4-5-0-3-1-5-6
  N14: Onderdeel1.D1/TX, Onderdeel2.connector1pad-47-4-0
  N15: Onderdeel1.D2, Onderdeel2.connector1pad-4-2-34-9, LCD1.DB7
  N16: Onderdeel1.D3_PWM, Onderdeel2.connector1pad-0-1-1-48, LCD1.DB6
  N17: Onderdeel1.D4, Onderdeel2.connector1pad-4-5-0-39-8, LCD1.DB5
  N18: Onderdeel1.D5_PWM, Onderdeel2.connector1pad-4-2-3-6-2, LCD1.DB4
  N19: Onderdeel1.D6_PWM, Onderdeel2.connector1pad-0-1-9-9-4, M1.D
  N20: Onderdeel1.D7, Onderdeel2.connector1pad-4-5-0-3-1-5, M1.B
  N21: Onderdeel1.RESET, Onderdeel2.connector1pad-4-5-0-3-1-5-3
  N22: Onderdeel1.3V3, Onderdeel2.connector1pad-0-1-9-9-4-6
  5V: Onderdeel1.5V, Onderdeel2.connector1pad-4-2-3-6-2-3, LCD1.VDD, R1.leg2
  N23: Onderdeel1.VIN, Onderdeel2.connector1pad-4-2-34-9-8
  N24: LCD1.E, R1.wiper
  N25: left.Pin_1, left.Pin_2
  N26: left.Pin_3, left.Pin_4
  N27: speed_up.Pin_1, speed_up.Pin_2
  N28: speed_up.Pin_3, speed_up.Pin_4
  N29: speed_down.Pin_1, speed_down.Pin_2
  N30: speed_down.Pin_3, speed_down.Pin_4
  N31: right.Pin_1, right.Pin_2
  N32: right.Pin_3, right.Pin_4
