# Fritzing sketch id3972_atmel_328_with_crystal_and_pins_0 (saved by Fritzing 0.8.3b)
circuit board: 16.9333cm x 5.64444cm
breadboards: 1

parts:
  U1 = atmega328 [package=dip]
  XTAL1 = Crystal [frequency="20 MHz" package=THT]
  S1 = Pushbutton [package=THT]
  U2 = Voltage Regulator - 5V [package="TO220 [THT]"]
  Power_plug1 = Power plug
  LCD1 = LCD screen
  S2 = Pushbutton [package="[THT]"]
  S3 = Pushbutton [package="[THT]"]
  S4 = Pushbutton [package="[THT]"]
  R1 = Rotary Potentiometer (Small)
  S5 = Toggle Switch [package=THT]
  C1 = Ceramic Capacitor [capacitance=22µF voltage=20V package="100 mil [THT, multilayer]"]
  C2 = Ceramic Capacitor [capacitance=22µF voltage=20V package="100 mil [THT, multilayer]"]

nets:
  N1: U1.RESET, S1.leg0
  N2: U1.XLAT1, XTAL1.pin_0, C2.0
  N3: U1.XLAT2, XTAL1.pin_1, C1.1
  GND: S1.leg1, U2.GND, LCD1.VSS, LCD1.LED-, R1.leg2, C1.0, C2.1
  N4: U2.input_voltage, Power_plug1.VCC
  N5: U2.output_voltage, LCD1.VDD, R1.leg1, S5.L2
  N6: LCD1.LED+, S5.COM
  N7: S2.Pin_1, S2.Pin_2
  N8: S2.Pin_3, S2.Pin_4
  N9: S3.Pin_1, S3.Pin_2
  N10: S3.Pin_3, S3.Pin_4
  N11: S4.Pin_1, S4.Pin_2
  N12: S4.Pin_3, S4.Pin_4
