# Fritzing sketch id3973_stepprv1_0 (saved by Fritzing 0.8.7b)
circuit board: 23.3123cm x 11.4032cm

parts:
  S1 = SWITCH-MOMENTARY-2 [package=tactile-pth-12mm]
  S2 = SWITCH-MOMENTARY-2 [package=tactile-pth-12mm]
  S3 = SWITCH-MOMENTARY-2 [package=tactile-pth-12mm]
  S4 = SWITCH-MOMENTARY-2 [package=tactile-pth-12mm]
  S5 = SWITCH-MOMENTARY-2 [package=tactile-pth-12mm]
  S6 = SWITCH-MOMENTARY-2 [package=tactile-pth-12mm]
  S7 = SWITCH-MOMENTARY-2 [package=tactile-pth-12mm]
  S8 = SWITCH-MOMENTARY-2 [package=tactile-pth-12mm]
  S9 = SWITCH-MOMENTARY-2 [package=tactile-pth-12mm]
  S10 = SWITCH-MOMENTARY-2 [package=tactile-pth-12mm]
  S11 = SWITCH-MOMENTARY-2 [package=tactile-pth-12mm]
  S12 = SWITCH-MOMENTARY-2 [package=tactile-pth-12mm]
  S13 = SWITCH-MOMENTARY-2 [package=tactile-pth-12mm]
  S14 = SWITCH-MOMENTARY-2 [package=tactile-pth-12mm]
  S15 = SWITCH-MOMENTARY-2 [package=tactile-pth-12mm]
  S16 = SWITCH-MOMENTARY-2 [package=tactile-pth-12mm]
  S17 = SWITCH-MOMENTARY-2 [package=tactile-pth-12mm]
  S18 = SWITCH-MOMENTARY-2 [package=tactile-pth-12mm]
  S19 = SWITCH-MOMENTARY-2 [package=tactile-pth-12mm]
  U5 = POT [package=alps_pot]
  U6 = POT [package=alps_pot]
  U7 = POT [package=alps_pot]
  U8 = POT [package=alps_pot]
  Teensy1 = Teensy 3.0

nets:
  N1: S1.1, S2.1, S3.1, S4.1, S5.1, S6.1, S7.1, S8.1, S9.1, S10.1, S11.1, S12.1, S13.1, S14.1, S15.1, S16.1, S17.1, S18.1, S19.1, Teensy1.GND
  N2: S1.2, Teensy1.D8
  N3: S2.2, Teensy1.D9
  N4: S3.2, Teensy1.D10
  N5: S4.2, Teensy1.D11
  N6: S5.2, Teensy1.D13
  N7: S6.2, Teensy1.D12
  N8: S7.2, Teensy1.A1/D15
  N9: S8.2, Teensy1.A0/D14
  N10: S9.2, Teensy1.D6
  N11: S10.2, Teensy1.D0
  N12: S11.2, Teensy1.D3
  N13: S12.2, Teensy1.D7
  N14: S13.2, Teensy1.D2
  N15: S14.2, Teensy1.D4
  N16: S15.2, Teensy1.D5
  N17: S16.2, Teensy1.D1
  N18: S17.2, Teensy1.A2/D16
  N19: S18.2, Teensy1.A3/D17
  N20: S19.2, Teensy1.A4/D18
  N21: U5.E, U6.E, U7.E, U8.E, Teensy1.Vin
  N22: U5.S, Teensy1.A8/D22
  N23: U5.A, U6.A, U7.A, U8.A, Teensy1.AGND
  N24: U6.S, Teensy1.A5/D19
  N25: U7.S, Teensy1.A7/D21
  N26: U8.S, Teensy1.A6/D20
