# Fritzing sketch id3974_Steuerung_RC_Auto_0 (saved by Fritzing 0.9.3b)
breadboards: 1

parts:
  Bauteil1 = Logic Level Converter
  Bauteil2 = Arduino Mega ADK (Rev3)
  Bauteil3 = SparkFun ESP8266 Thing
  U1 = LCD-16X2 [package=lcd-16x2]
  Bauteil4 = Tri-Axis Gyro Breakout - L3G4200D
  J1 = Basic Servo
  J2 = Basic Servo

nets:
  N1: Bauteil1.LV, Bauteil3.VIN
  N2: Bauteil1.RX_LV, Bauteil3.U0RXI
  N3: Bauteil1.TX_LV, Bauteil3.U0TXO
  N4: Bauteil1.TX_HV, Bauteil2.D1/TX0
  N5: Bauteil1.RX_HV, Bauteil2.D0/RX0
  VCC: Bauteil1.HV, Bauteil2.5V, U1.VDD, U1.A, Bauteil4.VCC, J1.vcc, J2.vcc
  GND: Bauteil1.GND, U1.VSS, U1.R_W, U1.K, J1.gnd, J2.gnd
  N6: Bauteil2.D21/SCL, Bauteil4.SCL
  N7: Bauteil2.D20/SDA, Bauteil4.SDA
  N8: Bauteil2.D12_PWM, U1.RS
  N9: Bauteil2.D11_PWM, U1.E
  N10: Bauteil2.D10_PWM, U1.DB4
  N11: Bauteil2.D9_PWM, U1.DB5
  N12: Bauteil2.D8_PWM, U1.DB6
  GND_2: Bauteil2.GND, Bauteil3.GND, Bauteil4.GND
  N13: Bauteil2.D2_PWM, Bauteil4.INT1
  N14: Bauteil2.D7_PWM, U1.DB7
  N15: Bauteil2.D22, J2.pulse
  N16: Bauteil2.D23, J1.pulse
