# Fritzing sketch id3975_Circuit_board_for_start_button_10_25_0 (saved by Fritzing 0.9.0b)
circuit board: 6.5cm x 6.1cm
breadboards: 1

parts:
  R1 = Resistor [tolerance=±5% resistance=10k package=THT]
  R2 = Resistor [tolerance=±5% resistance=10k package=THT]
  ATMega328 = atmega168 [package=dip]
  Interlock_switch = Screw terminal - 2 pins [package=THT]
  16Mhz = Crystal [frequency="16 Mhz" package=THT]
  Relay_Conn = RJ45 Jack [package=rj45-8]
  Start_Button = RJ45 Jack [package=rj45-8]
  R3 = Resistor [tolerance=±5% resistance=10k package=THT]
  Reset = Pushbutton [package="[THT]"]
  C1 = Tantalum Capacitor [capacitance=22pF package="100 mil [THT, tantalum]"]
  C2 = Tantalum Capacitor [capacitance=22pF package="100 mil [THT, tantalum]"]
  Pad1 = Pad [width=3 height=3 connect=center]  # not connected
  Pad2 = Pad [width=3 height=3 connect=center]  # not connected
  J2 = female pin header, 2 pins [form="♀ (female)"]
  J1 = female pin header, 2 pins [form="♀ (female)"]
  R4 = Resistor [tolerance=±5% resistance=220 package=THT]  # not connected
  LED1 = LED - 5mm [color="Red (633nm)" package="5 mm [THT]"]

nets:
  N1: R1.Pin_0, ATMega328.D3_(PWM), Start_Button.7
  N2: R1.Pin_1, R2.Pin_1, ATMega328.GND, Relay_Conn.1, Start_Button.1, Reset.Pin_3, Reset.Pin_4, C1.-, C2.-
  N3: R2.Pin_0, ATMega328.D2, Interlock_switch.pin1
  N4: ATMega328.RESET, R3.Pin_1, Reset.Pin_1, Reset.Pin_2
  N5: ATMega328.D0_(RX), J1.pin1
  N6: ATMega328.D1_(TX), J1.pin2
  N7: ATMega328.D4, LED1.anode
  N8: ATMega328.VCC, ATMega328.AVCC, ATMega328.AREF, Interlock_switch.pin2, Relay_Conn.3, Start_Button.3, Start_Button.5, R3.Pin_0
  N9: ATMega328.XLAT1, 16Mhz.pin_0, C2.+
  N10: ATMega328.XLAT2, 16Mhz.pin_1, C1.+
  N11: ATMega328.D5_(PWM), Relay_Conn.2
  N12: ATMega328.D6_(PWM), Relay_Conn.4
  N13: ATMega328.D7, Relay_Conn.8
  N14: ATMega328.D8, Relay_Conn.6
  N15: ATMega328.D9_(PWM), Relay_Conn.7
  N16: ATMega328.D10_(PWM), Start_Button.2
  N17: ATMega328.D11_(PWM), Start_Button.4
  N18: ATMega328.D12, Start_Button.6
  N19: ATMega328.D13, Start_Button.8
  N20: ATMega328.A1, J2.pin2
  N21: ATMega328.A2, J2.pin1

notes:
  civicjunkie.com
  +
  -
  5V DC
  A in
