# Fritzing sketch id3975_secuenciador_8_pasos (saved by Fritzing 0.5.2b)
breadboards: 4

parts:
  U1 = 555 Timer [package="DIP8 [THT]"]
  R1 = Resistor [resistance=1k package=THT]
  R3 = Rotary Potentiometer (Large) [package=THT]
  C1 = Electrolytic Capacitor [capacitance=100nF rated_voltage=35V package="100 mil [THT, electrolytic]"]  # not connected
  LED1 = Red LED - 5mm [package="5 mm [THT]"]
  R4 = Resistor [resistance=1k package=THT]
  IC1 = IC, DIP package, 16 pins [chip_label=4017 spacing=300mil]
  R5 = Rotary Potentiometer (Large) [package=THT]
  R6 = Rotary Potentiometer (Large) [package=THT]
  R7 = Rotary Potentiometer (Large) [package=THT]
  R8 = Rotary Potentiometer (Large) [package=THT]
  R9 = Rotary Potentiometer (Large) [package=THT]
  R10 = Rotary Potentiometer (Large) [package=THT]
  R11 = Rotary Potentiometer (Large) [package=THT]
  R12 = Rotary Potentiometer (Large) [package=THT]
  D1 = Rectifier Diode [package="300 mil [THT]"]
  D1_2 = Rectifier Diode [package="300 mil [THT]"]
  D1_3 = Rectifier Diode [package="300 mil [THT]"]
  D1_4 = Rectifier Diode [package="300 mil [THT]"]
  D1_5 = Rectifier Diode [package="300 mil [THT]"]
  D1_6 = Rectifier Diode [package="300 mil [THT]"]
  D1_7 = Rectifier Diode [package="300 mil [THT]"]
  D1_8 = Rectifier Diode [package="300 mil [THT]"]
  TRS1 = Stereo Jack (TRS) 3.5mm [package="PG203J [THT]"]
  Power_plug1 = Power plug
  LED2 = Red LED - 5mm [package="5 mm [THT]"]
  R13 = Resistor [resistance=1k package=THT]
  R13_2 = Resistor [resistance=1k package=THT]
  R13_3 = Resistor [resistance=1k package=THT]
  R13_4 = Resistor [resistance=1k package=THT]
  R13_5 = Resistor [resistance=1k package=THT]
  R13_6 = Resistor [resistance=1k package=THT]
  LED2_2 = Red LED - 5mm [package="5 mm [THT]"]
  LED2_3 = Red LED - 5mm [package="5 mm [THT]"]
  LED2_4 = Red LED - 5mm [package="5 mm [THT]"]
  LED2_5 = Red LED - 5mm [package="5 mm [THT]"]
  LED2_6 = Red LED - 5mm [package="5 mm [THT]"]
  LED2_7 = Red LED - 5mm [package="5 mm [THT]"]
  LED2_8 = Red LED - 5mm [package="5 mm [THT]"]
  R13_7 = Resistor [resistance=1k package=THT]
  R13_8 = Resistor [resistance=1k package=THT]
  C2 = Electrolytic Capacitor [capacitance=100nF rated_voltage=35V package="100 mil [THT, electrolytic]"]
  R14 = Resistor [resistance=220 package=THT]

nets:
  N1: U1.Threshold, R3.leg2
  N2: U1.Discharge, R1.Pin_1
  N3: U1.Vcc_Supply_Voltage, R1.Pin_0
  N4: R3.wiper, R14.Pin_1
  N5: LED1.cathode, R4.Pin_1
  N6: LED1.anode, IC1.pin14
  N7: R4.Pin_0, IC1.pin8, IC1.pin13, TRS1.Sleeve, Power_plug1.GND, R13.Pin_0, R13_2.Pin_0, R13_3.Pin_0, R13_4.Pin_0, R13_5.Pin_0, R13_6.Pin_0, R13_7.Pin_0, R13_8.Pin_0, C2.-
  N8: IC1.pin1, R10.leg2, LED2_6.anode
  N9: IC1.pin2, R6.leg2, LED2_2.anode
  N10: IC1.pin3, R5.leg2, LED2.anode
  N11: IC1.pin4, R7.leg2, LED2_3.anode
  N12: IC1.pin5, R11.leg2, LED2_7.anode
  N13: IC1.pin6, R12.leg2, LED2_8.anode
  N14: IC1.pin7, R8.leg2, R13_5.Pin_1, LED2_4.anode, LED2_5.cathode
  N15: IC1.pin9, IC1.pin15
  N16: IC1.pin10, R9.leg2, LED2_5.anode
  N17: IC1.pin16, Power_plug1.VCC, C2.+
  N18: R5.wiper, D1.anode
  N19: R6.wiper, D1_2.anode
  N20: R7.wiper, D1_3.anode
  N21: R8.wiper, D1_4.anode
  N22: R9.wiper, D1_7.anode
  N23: R10.wiper, D1_6.anode
  N24: R11.wiper, D1_5.anode
  N25: R12.wiper, D1_8.anode
  N26: D1.cathode, D1_2.cathode, D1_3.cathode, D1_4.cathode
  N27: D1_5.cathode, D1_6.cathode, D1_7.cathode, D1_8.cathode, TRS1.Ring
  N28: LED2.cathode, R13.Pin_1
  N29: R13_2.Pin_1, LED2_2.cathode
  N30: R13_3.Pin_1, LED2_3.cathode
  N31: R13_4.Pin_1, LED2_4.cathode
  N32: R13_6.Pin_1, LED2_6.cathode
  N33: LED2_7.cathode, R13_7.Pin_1
  N34: LED2_8.cathode, R13_8.Pin_1

notes:
  9v
  out
