# Fritzing sketch id3976_MiniSTMF4_02.june.2014_0 (saved by Fritzing 0.8.7b)
circuit board: 5.74154cm x 3.32343cm
breadboards: 1

parts:
  C3 = Ceramic Capacitor [capacitance=10pF package="0603 [SMD, multilayer]"]
  MicroUSB = USB Connectors [package=usb-microb]
  BOOT = SWITCH-MOMENTARY-2 [package=tactile_switch_smd-2]
  POWER = smd LED [color="Green (565nm)" part_number=Green package="1206 [SMD]"]
  R3 = Resistor [tolerance=±5% resistance=1k package="0805 [SMD]"]
  Fuse1 = Resettable Fuse PTC [part_number=600mA package=ptc-1206]
  R4 = Resistor [tolerance=±5% resistance=22 package="0805 [SMD]"]
  R5 = Resistor [tolerance=±5% resistance=22 package="0805 [SMD]"]
  R6 = Resistor [tolerance=±5% resistance=1.5k package="0805 [SMD]"]
  LED = smd LED [color="Red (633nm)" part_number=Red package="1206 [SMD]"]
  C13 = Ceramic Capacitor [capacitance=100nF package="0603 [SMD, multilayer]"]
  C15 = Ceramic Capacitor [capacitance=10µF package="0603 [SMD, multilayer]"]
  MC33269DT-3_3V = V_REG_MC33269 [part_number="(max 800mA out)" package=dpak]
  C18 = Ceramic Capacitor [capacitance=10µF package="0603 [SMD, multilayer]"]
  C2 = Ceramic Capacitor [capacitance=10pF package="0603 [SMD, multilayer]"]
  STM32F405RGT6 = STM32F40x [package="LQFP64, 10x10mm"]
  Reset = SWITCH-MOMENTARY-2 [package=tactile_switch_smd-2]
  R13 = Resistor [tolerance=±5% resistance=10k package="0805 [SMD]"]
  J2 = female pin header, 15 pins [form="♀ (female)"]
  J3 = female pin header, 15 pins [form="♀ (female)"]
  R9 = Resistor [tolerance=±5% resistance=10k package="0805 [SMD]"]
  C11 = Ceramic Capacitor [capacitance=100nF package="0603 [SMD, multilayer]"]
  R15 = Resistor [tolerance=±5% resistance=10k package="0805 [SMD]"]
  R2 = Resistor [tolerance=±5% resistance=10k package="0805 [SMD]"]
  R14 = Resistor [tolerance=±5% resistance=10k package="0805 [SMD]"]
  C5 = Ceramic Capacitor [capacitance=2.2µF package="0603 [SMD, multilayer]"]
  XTAL = CRYSTAL [part_number=25MHz package=crystal-smd-5x3]
  R1 = Resistor [tolerance=±5% resistance=390 package="0805 [SMD]"]
  R16 = Resistor [tolerance=±5% resistance=10k package="0805 [SMD]"]
  R10 = Resistor [tolerance=±5% resistance=10k package="0805 [SMD]"]
  C12 = Ceramic Capacitor [capacitance=100nF package="0603 [SMD, multilayer]"]
  C10 = Ceramic Capacitor [capacitance=100nF package="0603 [SMD, multilayer]"]
  C19 = Ceramic Capacitor [capacitance=10µF package="0603 [SMD, multilayer]"]
  C16 = Ceramic Capacitor [capacitance=10µF package="0603 [SMD, multilayer]"]
  C14 = Ceramic Capacitor [capacitance=100nF package="0603 [SMD, multilayer]"]
  R12 = Resistor [tolerance=±5% resistance=10k package="0805 [SMD]"]
  C4 = Ceramic Capacitor [capacitance=2.2µF package="0603 [SMD, multilayer]"]

nets:
  GND: C3.0, MicroUSB.GND, R3.Pin_1, R6.Pin_1, C13.0, C15.0, MC33269DT-3_3V.GND, C18.0, C2.0, STM32F405RGT6.VSSA, STM32F405RGT6.VSS1, STM32F405RGT6.VSS2, Reset.1, J2.pin2, C11.0, R15.Pin_1, R2.Pin_1, R14.Pin_1, C5.1, R16.Pin_1, R10.Pin_1, C12.0, C10.0, C19.0, C16.0, C14.0, C4.0
  N1: C3.1, XTAL.2, R1.Pin_0
  N2: MicroUSB.D+, R4.Pin_0
  N3: MicroUSB.D-, R5.Pin_0
  N4: MicroUSB.VBUS, Fuse1.1
  3.3V: BOOT.2, POWER.anode, C13.1, C15.1, MC33269DT-3_3V.OUT, STM32F405RGT6.VBAT, STM32F405RGT6.VDDA, STM32F405RGT6.VDD1, STM32F405RGT6.VDD2, STM32F405RGT6.VDD3, STM32F405RGT6.VDD4, R13.Pin_0, J2.pin1, R9.Pin_0, C11.1, C12.1, C10.1, C19.1, C16.1, C14.1, R12.Pin_0
  N5: BOOT.1, STM32F405RGT6.BOOT0, R2.Pin_0
  N6: POWER.cathode, R3.Pin_0
  USB VBUS: Fuse1.2, STM32F405RGT6.PA9
  USB Dplus: R4.Pin_1, STM32F405RGT6.PA12
  USB Dminus: R5.Pin_1, STM32F405RGT6.PA11
  N7: R6.Pin_0, LED.cathode
  LED: LED.anode, STM32F405RGT6.PA10, R9.Pin_1
  VIN: MC33269DT-3_3V.IN, C18.1, J3.pin1
  PH0: C2.1, STM32F405RGT6.PH0, XTAL.1
  N8: STM32F405RGT6.PC14, R14.Pin_0
  PH1: STM32F405RGT6.PH1, R1.Pin_1
  N9: STM32F405RGT6.NRST, Reset.2, R13.Pin_1
  Analog_0: STM32F405RGT6.PC0, J2.pin7
  Analog_1: STM32F405RGT6.PC1, J2.pin6
  Analog_2: STM32F405RGT6.PC2, J2.pin5
  Analog_3: STM32F405RGT6.PC3, J2.pin4
  Digital_8: STM32F405RGT6.PA0, J3.pin2
  Digital_7: STM32F405RGT6.PA1, J3.pin3
  Digital_3: STM32F405RGT6.PA2, J3.pin4
  Digital_2: STM32F405RGT6.PA3, J3.pin5
  Digital_9: STM32F405RGT6.PA6, J3.pin7
  Analog_4: STM32F405RGT6.PC4, J3.pin8
  Analog_5: STM32F405RGT6.PC5, J3.pin9
  N10: STM32F405RGT6.PB2, R10.Pin_0
  Digital_10: STM32F405RGT6.PB10, J3.pin10
  N11: STM32F405RGT6.PB11, R16.Pin_0
  N12: STM32F405RGT6.VCAP1, C4.1
  Digital_4: STM32F405RGT6.PB12, J3.pin11
  Digital_13: STM32F405RGT6.PB13, J3.pin12
  Digital_12: STM32F405RGT6.PB14, J3.pin13
  Digital_11: STM32F405RGT6.PB15, J3.pin14
  Digital_1: STM32F405RGT6.PC6, J3.pin15
  Digital_0: STM32F405RGT6.PC7, J2.pin14
  N13: STM32F405RGT6.VCAP2, C5.0
  N14: STM32F405RGT6.PC11, R15.Pin_0
  N15: STM32F405RGT6.PB5, R12.Pin_1
  SCL: STM32F405RGT6.PB6, J2.pin12
  SDA: STM32F405RGT6.PB7, J2.pin11
  Digital_5: STM32F405RGT6.PB8, J2.pin9
  Digital_6: STM32F405RGT6.PB9, J2.pin8

notes:
  Fnetduino, Custom Netduino board, Frode Lillerud. Uses Netduino 2 firmware., 30.05.2014
  Frode Lillerud
  02.june 2014
  STM32F405RGT6
  Digital 1
  Digital 11
  Digital 12
  Digital 13
  Digital 4
  Digital 10
  Analog 5
  Analog 4
  Digital 9
  NC
  Digital 2
  Digital 3
  Digital 7
  Digital 8
  VIN (4.4V-20V)
  3.3V
  Ground
  Digital 0
  I2C SDA
  I2C SCL
  Digital 5
  Digital 6
  Analog 0
  Analog 1
  Analog 2
  Analog 3
