# Fritzing sketch id3977_stompotto_0 (saved by Fritzing 0.7.10b)
breadboards: 1

parts:
  Arduino1 = Arduino
  LED1 = LED - 5mm [color="Blue (430nm)" package="5 mm [THT]"]
  LED2 = LED - 5mm [color="Blue (430nm)" package="5 mm [THT]"]
  LED3 = LED - 5mm [color="Blue (430nm)" package="5 mm [THT]"]
  LED4 = LED - 5mm [color="Blue (430nm)" package="5 mm [THT]"]
  LED5 = LED - 5mm [color="Blue (430nm)" package="5 mm [THT]"]
  LED6 = LED - 5mm [color="Blue (430nm)" package="5 mm [THT]"]
  LED7 = LED - 5mm [color="Blue (430nm)" package="5 mm [THT]"]
  LED8 = LED - 5mm [color="Blue (430nm)" package="5 mm [THT]"]
  S1 = Toggle Switch [package=THT]
  S2 = Toggle Switch [package=THT]
  S3 = Toggle Switch [package=THT]
  S4 = Toggle Switch [package=THT]
  S5 = Toggle Switch [package=THT]
  S6 = Toggle Switch [package=THT]
  S7 = Toggle Switch [package=THT]
  S8 = Toggle Switch [package=THT]
  R1 = Resistor [tolerance=±5% resistance=100 package=THT]
  R2 = Resistor [tolerance=±5% resistance=100 package=THT]
  R3 = Resistor [tolerance=±5% resistance=100 package=THT]
  R4 = Resistor [tolerance=±5% resistance=100 package=THT]
  R5 = Resistor [tolerance=±5% resistance=100 package=THT]
  R6 = Resistor [tolerance=±5% resistance=100 package=THT]
  R7 = Resistor [tolerance=±5% resistance=100 package=THT]
  R8 = Resistor [tolerance=±5% resistance=100 package=THT]

nets:
  N1: Arduino1.D9, S8.COM, R8.Pin_1
  N2: Arduino1.D8, S7.COM, R7.Pin_1
  N3: Arduino1.D7, S6.COM, R6.Pin_1
  N4: Arduino1.D6, S5.COM, R5.Pin_1
  N5: Arduino1.D5, S4.COM, R4.Pin_1
  N6: Arduino1.D4, S3.COM, R3.Pin_1
  N7: Arduino1.D3, S2.COM, R2.Pin_1
  N8: Arduino1.D2, S1.COM, R1.Pin_1
  N9: Arduino1.+5V, S1.L2, S2.L2, S3.L2, S4.L2, S5.L2, S6.L2, S7.L2, S8.L2
  N10: Arduino1.GND, LED1.cathode, LED2.cathode, LED3.cathode, LED4.cathode, LED5.cathode, LED6.cathode, LED7.cathode, LED8.cathode, S1.L1, S2.L1, S3.L1, S4.L1, S5.L1, S6.L1, S7.L1, S8.L1
  N11: LED1.anode, R1.Pin_0
  N12: LED2.anode, R2.Pin_0
  N13: LED3.anode, R3.Pin_0
  N14: LED4.anode, R4.Pin_0
  N15: LED5.anode, R5.Pin_0
  N16: LED6.anode, R6.Pin_0
  N17: LED7.anode, R7.Pin_0
  N18: LED8.anode, R8.Pin_0
