# Fritzing sketch id3978_Stop_Lights_0 (saved by Fritzing 0.8.7b)
circuit board: 8.46667cm x 5.64444cm
breadboards: 1

parts:
  100Ω = Resistor [tolerance=±5% resistance=100 package=THT]
  100Ω_2 = Resistor [tolerance=±5% resistance=100 package=THT]
  LED_R = LED - 5mm [color="Red (633nm)" package="5 mm [THT]"]
  LED_R_2 = LED - 5mm [color="Red (633nm)" package="5 mm [THT]"]
  LED_R_3 = LED - 5mm [color="Red (633nm)" package="5 mm [THT]"]
  LED_Y = LED - 5mm [color="Yellow (585nm)" package="5 mm [THT]"]
  LED_Y_2 = LED - 5mm [color="Yellow (585nm)" package="5 mm [THT]"]
  LED_Y_3 = LED - 5mm [color="Yellow (585nm)" package="5 mm [THT]"]
  LED_G = LED - 5mm [color="Green (555nm)" package="5 mm [THT]"]
  LED_G_2 = LED - 5mm [color="Green (555nm)" package="5 mm [THT]"]
  LED_G_3 = LED - 5mm [color="Green (555nm)" package="5 mm [THT]"]
  LED_G_4 = LED - 5mm [color="Green (555nm)" package="5 mm [THT]"]
  LED_G_5 = LED - 5mm [color="Green (555nm)" package="5 mm [THT]"]
  LED_Y_4 = LED - 5mm [color="Yellow (585nm)" package="5 mm [THT]"]
  LED_Y_5 = LED - 5mm [color="Yellow (585nm)" package="5 mm [THT]"]
  LED_R_4 = LED - 5mm [color="Red (633nm)" package="5 mm [THT]"]
  LED_R_5 = LED - 5mm [color="Red (633nm)" package="5 mm [THT]"]
  100Ω_3 = Resistor [tolerance=±5% resistance=100 package=THT]
  Arduino_Uno = Arduino Uno (Rev3)

nets:
  N1: 100Ω.Pin_0, LED_Y.anode, LED_Y_2.anode, LED_Y_3.anode, LED_Y_4.anode, LED_Y_5.anode
  N2: 100Ω.Pin_1, 100Ω_2.Pin_1, 100Ω_3.Pin_1, Arduino_Uno.GND
  N3: 100Ω_2.Pin_0, LED_G.anode, LED_G_2.anode, LED_G_3.anode, LED_G_4.anode, LED_G_5.anode
  N4: LED_R.cathode, LED_R_2.cathode, LED_R_3.cathode, LED_R_4.cathode, LED_R_5.cathode, Arduino_Uno.D2
  N5: LED_R.anode, LED_R_2.anode, LED_R_3.anode, LED_R_4.anode, LED_R_5.anode, 100Ω_3.Pin_0
  N6: LED_Y.cathode, LED_Y_2.cathode, LED_Y_3.cathode, LED_Y_4.cathode, LED_Y_5.cathode, Arduino_Uno.D3_PWM
  N7: LED_G.cathode, LED_G_2.cathode, LED_G_3.cathode, LED_G_4.cathode, LED_G_5.cathode, Arduino_Uno.D4
