# Fritzing sketch id3979_secundomer_with_button_0 (saved by Fritzing 0.9.3b)
breadboards: 1

parts:
  R1 = Resistor [tolerance=±5% resistance=220 package=THT]
  R2 = Resistor [tolerance=±5% resistance=220 package=THT]
  R3 = Resistor [tolerance=±5% resistance=220 package=THT]  # not connected
  R4 = Resistor [tolerance=±5% resistance=220 package=THT]  # not connected
  R5 = Resistor [tolerance=±5% resistance=220 package=THT]  # not connected
  R6 = Resistor [tolerance=±5% resistance=220 package=THT]
  R7 = Resistor [tolerance=±5% resistance=220 package=THT]
  U1 = 7-SEGMENT-DISPLAY [package=7-segment-display]
  S1 = Pushbutton [package="[THT]"]
  Часть1 = Arduino Uno (Rev3)

nets:
  N1: R1.Pin_0, Часть1.D2
  N2: R1.Pin_1, U1.D
  N3: R2.Pin_0, U1.G1
  N4: R2.Pin_1, Часть1.D4
  N5: R6.Pin_0, Часть1.D8
  N6: R6.Pin_1, U1.E
  N7: R7.Pin_0, Часть1.D7
  N8: R7.Pin_1, U1.G
  N9: U1.F, S1.Pin_1, S1.Pin_2, Часть1.GND
  N10: S1.Pin_3, S1.Pin_4, Часть1.D9_PWM
