# Fritzing sketch id397_MQ_2_Breadboard_0 (saved by Fritzing 0.7.12b)
breadboards: 1

parts:
  Arduino1 = Arduino
  R1 = Resistor [tolerance=±5% resistance=22k package=THT]

nets:
  N1: Arduino1.GND, R1.Pin_1
  N2: Arduino1.A0, R1.Pin_0

notes:
  MQ-2 Sensor Pins
  A B
  H H
  A B
  MQ-2 Sensor Wires
  R G
  R W
  R G
  Red wires connected to both A pins and the left H pin and running to the 5V pin on the Arduino
  Green wires connected to both B pins and running to the analog pin A0 on the Arduino
  White wire connected to the right B pin and running to GND on the Arduino.
  A 22K ohms resistor connected to the green wires (analog pin) and the white wire (ground).
  Arduino Uno + MQ-2 (gas & smoke) Sensor
  Derek Erb - 26/02/2013
  http://about.me/derekerb
  derek.erb@gmail.com
