# Fritzing sketch id3980_stormshutter_0 (saved by Fritzing 0.8.7b)
breadboards: 1

parts:
  U2 = Optocoupler [package=THT]
  R9 = Resistor [tolerance=±1% resistance=54.9 package=THT]
  Componente2 = Arduino Nano (Rev3.0)
  R10 = Resistor [tolerance=±1% resistance=54.9 package=THT]

nets:
  N1: U2.Pin_1, Componente2.D13/SCK
  N2: U2.Pin_2, R10.Pin_0
  N3: U2.Pin_4, R9.Pin_0
  Cam Foccus +/Cam Shutter +: U2.Pin_5
  Cam Gnd: R9.Pin_1
  Sensor Gnd: Componente2.GND, R10.Pin_1
  Sensor Vcc: Componente2.5V
  Sensor Out: Componente2.A5

notes:
  Cam Gnd
  Cam Foccus +
  Cam Shutter +
  Sensor Vcc
  Sensor Out
  Sensor Gnd
