# Fritzing sketch id3981_Straight_Key_Oscillator_0 (saved by Fritzing 0.9.3b)
breadboards: 1

parts:
  Part2 = Arduino Mega 2560 (Rev3)
  R1 = Resistor [tolerance=±5% resistance=10 package=THT]
  S1 = Round Pushbutton
  R3 = Rotary Potentiometer (Small) [maximum_resistance=100kΩ package=THT]
  SPKR1 = Loudspeaker

nets:
  N1: Part2.D8_PWM, R3.wiper
  N2: Part2.5V, S1.leg0
  N3: Part2.GND, R1.Pin_1, SPKR1.pin1
  N4: Part2.D2_PWM, R1.Pin_0, S1.leg1
  N5: R3.leg1, SPKR1.pin2
