# Fritzing sketch id3983_strobo_0 (saved by Fritzing 0.8.5b)

parts:
  IC1 = General purpose bipolar Timer [package=dil-08]
  J1 = Screw terminal - 2 pins [package=THT]
  R1 = Resistor [tolerance=±5% resistance=470 package=THT]
  R2 = Rotary Potentiometer (Small) [maximum_resistance=10kΩ package=THT]
  R3 = Resistor [tolerance=±5% resistance=10 package=THT]
  C1 = Electrolytic Capacitor [capacitance=100nF voltage=35V package="100 mil [THT, electrolytic]"]
  LED1 = LED - 5mm [color="White (8000K)" package="5 mm [THT]"]
  R4 = Resistor [tolerance=±5% resistance=470 package=THT]

nets:
  N1: IC1.GND, J1.pin2, C1.-
  N2: IC1.TRI, IC1.TRE, R3.Pin_1, C1.+
  N3: IC1.OUT, R4.Pin_1
  N4: IC1._RES, IC1.VCC+, J1.pin1, R1.Pin_0, LED1.cathode
  N5: IC1.DIS, R2.leg1, R3.Pin_0
  N6: R1.Pin_1, R2.wiper, R2.leg2
  N7: LED1.anode, R4.Pin_0

notes:
  +
  -
  12 V
  potenziometro 10 Kohm
  condensatore 100 uF
  resistenza led
  ne555
