# Fritzing sketch id3984_ultra_0 (saved by Fritzing 0.9.2b)
breadboards: 1

parts:
  Onderdeel1 = Arduino Nano (Rev3.0)
  Onderdeel2 = SRF05 Ultrasonic Rangefinder

nets:
  N1: Onderdeel1.GND, Onderdeel2.connector11
  N2: Onderdeel1.D2, Onderdeel2.connector9
  N3: Onderdeel1.D3, Onderdeel2.connector10
  N4: Onderdeel1.5V, Onderdeel2.connector8
