# Fritzing sketch id3985_proecto_musical_doris_0 (saved by Fritzing 0.7.5b)
breadboards: 1

parts:
  R1 = Resistor [tolerance=±5% resistance=220 package=THT]
  R2 = Resistor [tolerance=±5% resistance=220 package=THT]
  LED1 = LED - 5mm [color="Red (633nm)" package="5 mm [THT]"]
  J1 = Piezo Speaker
  LED2 = LED - 5mm [color="Red (633nm)" package="5 mm [THT]"]
  Arduino1 = Arduino

nets:
  N1: R1.Pin_0, R2.Pin_0, J1.pin1, Arduino1.3V3
  N2: R1.Pin_1, LED1.cathode
  N3: R2.Pin_1, LED2.cathode
  N4: LED1.anode, Arduino1.D11
  N5: J1.pin2, Arduino1.D13
  N6: LED2.anode, Arduino1.D12
