# Fritzing sketch id3986_suenan_las_campanas_0 (saved by Fritzing 0.7.5b)
breadboards: 1

parts:
  Arduino1 = Arduino
  LED1 = LED - 5mm [color="Red (633nm)" package="5 mm [THT]"]
  R1 = Resistor [tolerance=±5% resistance=220 package=THT]
  R2 = Resistor [tolerance=±5% resistance=220 package=THT]
  LED2 = LED - 5mm [color="Red (633nm)" package="5 mm [THT]"]
  J1 = Piezo Speaker

nets:
  N1: Arduino1.D13, LED1.anode
  N2: Arduino1.D12, LED2.anode
  N3: Arduino1.D8, J1.pin2
  N4: Arduino1.GND, R1.Pin_1, R2.Pin_1, J1.pin1
  N5: LED1.cathode, R1.Pin_0
  N6: R2.Pin_0, LED2.cathode
