# Fritzing sketch id3987_Sunbador_ultra_0 (saved by Fritzing 0.7.5b)
breadboards: 1

parts:
  Arduino1 = Arduino
  LED1 = LED - 5mm [color="Red (633nm)" package="5 mm [THT]"]
  R1 = Resistor [tolerance=±5% resistance=220 package=THT]
  R2 = Resistor [tolerance=±5% resistance=220 package=THT]
  LED2 = LED - 5mm [color="Red (633nm)" package="5 mm [THT]"]
  J1 = Piezo Speaker
  Parte3 = HC-SR04 ultrasonic distance sensor

nets:
  N1: Arduino1.D13, LED1.anode
  N2: Arduino1.D12, LED2.anode
  N3: Arduino1.D8, J1.pin2
  N4: Arduino1.D7, Parte3.connector0
  N5: Arduino1.+5V, Parte3.connector1
  N6: Arduino1.GND, R1.Pin_1, R2.Pin_1, J1.pin1, Parte3.connector2
  N7: LED1.cathode, R1.Pin_0
  N8: R2.Pin_0, LED2.cathode
