# Fritzing sketch id3988_Untitled_Sketch_0 (saved by Fritzing 0.9.3b)
perfboards: 1

parts:
  Part1 = Arduino Nano (Rev3.0)
  M1 = DC Motor  # not connected
  M2 = DC Motor  # not connected
  R1 = Photocell (LDR) [package=THT]
  R2 = Photocell (LDR) [package=THT]
  VCC1 = Battery block 9V
  Q1 = PNP-Transistor [package="TO92 [THT]"]
  Q2 = PNP-Transistor [package="TO92 [THT]"]
  Q3 = PNP-Transistor [package="TO92 [THT]"]
  Q4 = PNP-Transistor [package="TO92 [THT]"]
  Q5 = PNP-Transistor [package="TO92 [THT]"]
  Q6 = PNP-Transistor [package="TO92 [THT]"]
  Q7 = PNP-Transistor [package="TO92 [THT]"]
  Q8 = PNP-Transistor [package="TO92 [THT]"]

nets:
  N1: Part1.GND, VCC1.+
  N2: Part1.D4, R2.pin_0
  N3: Part1.D5, R1.pin_0
  N4: Part1.VIN, VCC1.-
  N5: R1.pin_1, Q1.E, Q3.C
  N6: Q1.C, Q2.E
  N7: Q2.C, Q4.E
  N8: Q3.E, Q4.C
  N9: Q5.E, Q7.C
  N10: Q5.C, Q6.E
  N11: Q6.C, Q8.E
  N12: Q7.E, Q8.C
