# Fritzing sketch id3989_sumba_wiring_0 (saved by Fritzing 0.7.12b)
breadboards: 2

parts:
  VCC1 = 4 x AAA Battery Mount
  Arduino1 = Arduino
  M1 = DC Motor
  M2 = DC Motor
  Q1 = NPN-Transistor [package="TO92 [THT]"]
  Q2 = NPN-Transistor [package="TO92 [THT]"]
  J1 = Infrared Proximity Sensor
  J2 = Infrared Proximity Sensor
  J3 = Infrared Proximity Sensor

nets:
  GND: VCC1.-, Arduino1.GND, M1.pin_1, M2.pin_1, J1.GND, J2.GND, J3.GND
  N1: VCC1.+, Q1.E, Q2.E
  N2: Arduino1.D6, Q1.B
  N3: Arduino1.D5, Q2.B
  VCC: Arduino1.+5V, J1.Vcc, J2.Vcc, J3.Vcc
  N4: Arduino1.A0, J3.Vout
  N5: Arduino1.A1, J2.Vout
  N6: Arduino1.A2, J1.Vout
  N7: M1.pin_2, Q2.C
  N8: M2.pin_2, Q1.C
