# Fritzing sketch id398_Panser_0 (saved by Fritzing 0.8.7b)
breadboards: 1

parts:
  Arduino = Arduino Uno (Rev3)
  U1 = 555 Timer [package="DIP8 [THT]"]
  U2 = 555 Timer [package="DIP8 [THT]"]
  Left_Motor = DC Motor
  Right_Motor = DC Motor
  U4 = 555 Timer [package="DIP8 [THT]"]
  JY-MCU = ArduinoBluetoothMatev13.fzp
  Battery = Battery block 9V
  U3 = 555 Timer [package="DIP8 [THT]"]

nets:
  N1: Arduino.GND, U1.Ground, U2.Ground, U4.Ground, JY-MCU.connector17, Battery.-, U3.Ground
  N2: Arduino.D0/RX, JY-MCU.connector14
  N3: Arduino.D1/TX, JY-MCU.connector16
  N4: Arduino.D2, U1.Control_Voltage, U2.Control_Voltage
  N5: Arduino.D3_PWM, U1.Trigger, U1.Threshold
  N6: Arduino.D4, U4.Control_Voltage, U3.Control_Voltage
  N7: Arduino.D5_PWM, U3.Trigger, U3.Threshold
  N8: Arduino.5V, JY-MCU.connector15
  N9: Arduino.VIN, U1.Reset, U1.Vcc_Supply_Voltage, U2.Reset, U2.Vcc_Supply_Voltage, U4.Reset, U4.Vcc_Supply_Voltage, Battery.+, U3.Reset, U3.Vcc_Supply_Voltage
  N10: U1.Output, U2.Trigger, U2.Threshold, Left_Motor.pin_1
  N11: U2.Output, Left_Motor.pin_2
  N12: Right_Motor.pin_1, U4.Trigger, U4.Threshold, U3.Output
  N13: Right_Motor.pin_2, U4.Output
