# Fritzing sketch id3990_Thesis_PCB_0 (saved by Fritzing 0.9.3b)
breadboards: 1

parts:
  Part1 = Arduino Micro (Rev3)
  J1 = Basic Servo
  J2 = Basic Servo
  R1 = Photocell (LDR) [package=THT]
  R2 = Photocell (LDR) [package=THT]
  R3 = Photocell (LDR) [package=THT]
  R4 = Photocell (LDR) [package=THT]
  R5 = Resistor [tolerance=±5% resistance=220 package="0603 [SMD]"]
  R6 = Resistor [tolerance=±5% resistance=220 package="0603 [SMD]"]
  R7 = Resistor [tolerance=±5% resistance=220 package="0603 [SMD]"]
  R8 = Resistor [tolerance=±5% resistance=220 package="0603 [SMD]"]
  Part2 = Triple Axis Gyro Breakout ITG-3200
  Raspberry_Pi_1 = Raspberry Pi 3 [part_number=RPI-3-V1.2]
  ZS-042_RTC1 = ZS-042 RTC Module

nets:
  N1: Part1.D2/SDA, Raspberry_Pi_1.GPIO26
  N2: Part1.D3/SCL, Raspberry_Pi_1.GPIO19
  N3: Part1.D4_PWM/A6, Raspberry_Pi_1.GPIO13
  N4: Part1.D11_PWM, J2.pulse
  N5: Part1.D12_PWM/A11, J1.pulse
  N6: Part1.SCK, Part2.SCL
  N7: Part1.MISO, Part2.SDA
  GND: Part1.GND, J1.gnd, J2.gnd, R5.Pin_0, R6.Pin_0, R7.Pin_1, R8.Pin_1, Part2.GND, Raspberry_Pi_1.GND, ZS-042_RTC1.GND
  VCC: Part1.5V, J1.vcc, J2.vcc
  N8: Part1.A3, R4.pin_1, R8.Pin_0
  N9: Part1.A2, R2.pin_1, R7.Pin_0
  N10: Part1.A1, R1.pin_1, R6.Pin_1
  N11: Part1.A0, R3.pin_1, R5.Pin_1
  3V3: Part1.3V3, Part2.VCC
  N12: R1.pin_0, R2.pin_0, R3.pin_0, R4.pin_0
  3V3_2: Raspberry_Pi_1.3v3, ZS-042_RTC1.VCC
  N13: Raspberry_Pi_1.GPIO2, ZS-042_RTC1.SDA
  N14: Raspberry_Pi_1.GPIO3, ZS-042_RTC1.SCL
