# Fritzing sketch id3991_devre_board_0 (saved by Fritzing 0.9.3b)
breadboards: 1

parts:
  R1 = Resistor [tolerance=±5% resistance=2.2k package=THT]
  VCC1 = Battery block 9V
  R3 = Resistor [tolerance=±5% resistance=3.3k package=THT]
  R2 = Resistor [tolerance=±5% resistance=680 package=THT]
  R4 = Resistor [tolerance=±5% resistance=4.7k package=THT]

nets:
  N1: R1.Pin_0, VCC1.+
  N2: R1.Pin_1, R3.Pin_1, R2.Pin_0
  N3: VCC1.-, R3.Pin_0, R4.Pin_0
  N4: R2.Pin_1, R4.Pin_1
