# Fritzing sketch id3992_Simple_Motor_Controller_0 (saved by Fritzing 0.9.2b)
breadboards: 1

parts:
  Part1 = Arduino Uno (Rev3)
  R1 = Resistor [tolerance=±5% resistance=1k package=THT]
  D1 = Rectifier Diode [part_number=1N4001 package="300 mil [THT]"]
  M1 = DC Motor
  Q1 = npn-Powertransistor [part_number="TIP120 from Adafruit PRODUCT ID: 976" package="TO220 [THT]"]
  VCC1 = Battery block 9V

nets:
  N1: Part1.D3_PWM, R1.Pin_0
  N2: Part1.GND, Q1.emitter, VCC1.-
  N3: Part1.VIN, D1.cathode, M1.pin_1, VCC1.+
  N4: R1.Pin_1, Q1.base
  N5: D1.anode, M1.pin_2, Q1.collector
