# Fritzing sketch id3993_SweetMaker_FizzyMint_0 (saved by Fritzing 0.9.3b)
circuit board: 8.46667cm x 5.64444cm

parts:
  Arduino_Nano_V3 = Arduino Nano (Rev3.0)
  Piezo_Element_1 = Piezo Speaker
  LED3 = LED - 3mm [color="Blue (505nm)" package="3 mm [THT]"]
  LED1 = LED - 3mm [color="Red (635nm)" package="3 mm [THT]"]
  LED2 = LED - 3mm [color="Green (565nm)" package="3 mm [THT]"]
  R2 = Resistor [tolerance=±20% resistance=220 package=THT]
  R1 = Resistor [tolerance=±5% resistance=220 package=THT]
  R3 = Resistor [tolerance=±5% resistance=220 package=THT]
  Switch_1 = Pushbutton [package="[THT]"]

nets:
  N1: Arduino_Nano_V3.D2, Switch_1.Pin_1, Switch_1.Pin_2
  N2: Arduino_Nano_V3.D3, Switch_1.Pin_3, Switch_1.Pin_4
  N3: Arduino_Nano_V3.D4, LED2.cathode
  N4: Arduino_Nano_V3.D5, R3.Pin_1
  N5: Arduino_Nano_V3.D6, R1.Pin_1
  N6: Arduino_Nano_V3.D7, LED1.cathode
  N7: Arduino_Nano_V3.D11/MOSI, R2.Pin_1
  N8: Arduino_Nano_V3.D12/MISO, LED3.cathode
  N9: Arduino_Nano_V3.A3, Piezo_Element_1.pin1
  N10: Arduino_Nano_V3.A2, Piezo_Element_1.pin2
  N11: LED3.anode, R2.Pin_0
  N12: LED1.anode, R1.Pin_0
  N13: LED2.anode, R3.Pin_0
