# Fritzing sketch id3995_Switch_Control_Press_0 (saved by Fritzing 0.9.1b)
breadboards: 1

parts:
  Parte1 = Arduino Uno (Rev3)
  R1 = Resistor [tolerance=±5% resistance=10k package=THT]
  R2 = Resistor [tolerance=±5% resistance=330 package=THT]
  LED1 = LED - 5mm [color="Red (633nm)" package="5 mm [THT]"]
  S2 = Pushbutton [package=THT]

nets:
  N1: Parte1.D8, R1.Pin_0, S2.leg0
  N2: Parte1.D4, LED1.anode
  N3: Parte1.5V, S2.leg1
  N4: Parte1.GND, R1.Pin_1, R2.Pin_1
  N5: R2.Pin_0, LED1.cathode
