# Fritzing sketch id3996_ETS2_HID_device_0 (saved by Fritzing 0.9.3b)
breadboards: 1

parts:
  U1 = atmega168 [package=dip]
  S2 = Taiway 100-SP-X-T1 SPDT Miniature Toggle Switch [part_number=100-SP-X-T1-0-0-B1-M1 package=THT]
  S3 = Taiway 100-SP-X-T1 SPDT Miniature Toggle Switch [part_number=100-SP-X-T1-0-0-B1-M1 package=THT]
  S4 = Round Pushbutton
  U3 = Mini-USB _B_ connector with 5th pin broken out. [package=usb-minib]
  S7 = SWITCH-SP3T [package=switch-sp3t-smd]

nets:
  N1: U1.RESET, U3.ID
  N2: U1.D0_(RX), U3.GND
  N3: U1.D2, S2.L1
  N4: U1.D3_(PWM), S3.L1
  N5: U1.VCC, U1.AVCC, U3.VBUS
  N6: U1.GND, S2.L2, S3.L2, S4.leg1, U3.D-, S7.2
  N7: U1.D5_(PWM), S4.leg0
  N8: U1.A0, S7.1
  N9: U1.A1, S7.4

notes:
  Kierunkowskaz [2 pozycje i "neutral"]
  Engine
  Światła
  USB
  Nowsza wersja ATmega8
