# Fritzing sketch id3997_Switch_usb_0 (saved by Fritzing 0.9.3b)

parts:
  X2 = USB Connectors [package=usb-a-s-nosilk-female]
  X1 = USB Connectors [package=usb-a-s-nosilk]
  X3 = USB Connectors [package=usb-a-s-silk-female]
  X4 = USB Connectors [package=usb-a-s-silk-female]
  X5 = USB Connectors [package=usb-a-s-silk-female]
  X6 = USB Connectors [package=usb-a-s-silk-female]
  S1 = SPST Switch [package=switche-dpdt]

nets:
  N1: X2.D+, X1.D+, S1.P
  N2: X2.D-, X3.D-, X6.D-
  GND: X2.GND, X3.GND, X6.GND
  N3: X2.VBUS, X3.VBUS, X6.VBUS
  N4: X1.D-, X4.D-, X5.D-
  GND_2: X1.GND, X4.GND, X5.GND
  N5: X1.VBUS, X4.VBUS, X5.VBUS
  N6: X3.D+, X4.D+, S1.O
  N7: X5.D+, X6.D+, S1.S
