# Fritzing sketch id3998_switch_and_led_0 (saved by Fritzing 0.9.3b)
circuit board: 8.16273cm x 5.31517cm
breadboards: 1

parts:
  SparkFun_Pro_Micro1 = 5v [part_number=DEV-12640]
  R1 = Resistor [tolerance=±5% resistance=10k package=THT]
  S2 = Pushbutton [package="[THT]"]
  LED1 = LED - 5mm [color="Red (633nm)" package="5 mm [THT]"]
  R2 = Resistor [tolerance=±5% resistance=220 package=THT]

nets:
  N1: SparkFun_Pro_Micro1.connector29, SparkFun_Pro_Micro1.connector48, R1.Pin_1, LED1.cathode
  N2: SparkFun_Pro_Micro1.connector31, S2.Pin_3, S2.Pin_4
  N3: SparkFun_Pro_Micro1.connector39, R2.Pin_0
  N4: SparkFun_Pro_Micro1.connector40, R1.Pin_0, S2.Pin_1, S2.Pin_2
  N5: LED1.anode, R2.Pin_1
