# Fritzing sketch id3999_connect_switch_led_0 (saved by Fritzing 0.9.3b)
breadboards: 1

parts:
  パーツ1 = Arduino Uno (Rev3)
  R1 = Resistor [tolerance=±5% resistance=180 package=THT]
  LED1 = LED - 5mm [color="Red (633nm)" package="5 mm [THT]"]
  S1 = Pushbutton [package="[THT]"]
  R2 = Resistor [tolerance=±5% resistance=10k package=THT]

nets:
  N1: パーツ1.D13/SCK, R1.Pin_0
  N2: パーツ1.GND, LED1.cathode, R2.Pin_1
  N3: パーツ1.D2, S1.Pin_1, S1.Pin_2, R2.Pin_0
  N4: パーツ1.5V, S1.Pin_3, S1.Pin_4
  N5: R1.Pin_1, LED1.anode
