# Fritzing sketch id39_MOSFET_solenoid_driver_board_0 (saved by Fritzing 0.9.3b)
circuit board: 13.3867cm x 3.23422cm
breadboards: 1

parts:
  D1 = Rectifier Diode [part_number=1N4001 package="300 mil [THT]"]
  Q2 = npn-Powertransistor [package="TO220 [THT]"]
  Q3 = npn-Powertransistor [package="TO220 [THT]"]
  D2 = Rectifier Diode [part_number=1N4001 package="300 mil [THT]"]
  Q4 = npn-Powertransistor [package="TO220 [THT]"]
  Q5 = npn-Powertransistor [package="TO220 [THT]"]
  D3 = Rectifier Diode [part_number=1N4001 package="300 mil [THT]"]
  D4 = Rectifier Diode [part_number=1N4001 package="300 mil [THT]"]
  Q6 = npn-Powertransistor [package="TO220 [THT]"]
  Q7 = npn-Powertransistor [package="TO220 [THT]"]
  D5 = Rectifier Diode [part_number=1N4001 package="300 mil [THT]"]
  D6 = Rectifier Diode [part_number=1N4001 package="300 mil [THT]"]
  Q8 = npn-Powertransistor [package="TO220 [THT]"]
  Q9 = npn-Powertransistor [package="TO220 [THT]"]
  D7 = Rectifier Diode [part_number=1N4001 package="300 mil [THT]"]
  D8 = Rectifier Diode [part_number=1N4001 package="300 mil [THT]"]
  J11 = male pin header, 4 pins [form="♂ (male)"]
  J12 = male pin header, 4 pins [form="♂ (male)"]
  J13 = male pin header, 4 pins [form="♂ (male)"]
  J14 = male pin header, 4 pins [form="♂ (male)"]
  J3 = screw terminal, 8 pins
  J15 = screw terminal, 8 pins
  Q10 = npn-Powertransistor [package="TO220 [THT]"]
  Q11 = npn-Powertransistor [package="TO220 [THT]"]
  Q12 = npn-Powertransistor [package="TO220 [THT]"]
  Q13 = npn-Powertransistor [package="TO220 [THT]"]
  Q14 = npn-Powertransistor [package="TO220 [THT]"]
  Q15 = npn-Powertransistor [package="TO220 [THT]"]
  Q16 = npn-Powertransistor [package="TO220 [THT]"]
  Q17 = npn-Powertransistor [package="TO220 [THT]"]
  D9 = Rectifier Diode [part_number=1N4001 package="300 mil [THT]"]
  D10 = Rectifier Diode [part_number=1N4001 package="300 mil [THT]"]
  D11 = Rectifier Diode [part_number=1N4001 package="300 mil [THT]"]
  D12 = Rectifier Diode [part_number=1N4001 package="300 mil [THT]"]
  D13 = Rectifier Diode [part_number=1N4001 package="300 mil [THT]"]
  D14 = Rectifier Diode [part_number=1N4001 package="300 mil [THT]"]
  D15 = Rectifier Diode [part_number=1N4001 package="300 mil [THT]"]
  D16 = Rectifier Diode [part_number=1N4001 package="300 mil [THT]"]
  J16 = screw terminal, 8 pins
  J17 = screw terminal, 8 pins
  J18 = screw terminal, 2 pins

nets:
  N1: D1.cathode, J15.pin8
  N2: D1.anode, Q2.collector
  N3: Q2.base, J11.pin4
  N4: Q2.emitter, Q4.emitter, Q5.emitter, Q6.emitter, Q7.emitter, Q8.emitter, Q9.emitter, Q10.emitter, Q11.emitter, Q12.emitter, Q13.emitter, Q14.emitter, Q15.emitter, Q16.emitter, Q17.emitter, J18.pin2
  N5: Q3.base, J11.pin3
  N6: Q3.collector, D2.anode
  N7: D2.cathode, J15.pin6
  N8: Q4.base, J11.pin1
  N9: Q4.collector, D4.anode
  N10: Q5.base, J11.pin2
  N11: Q5.collector, D3.anode
  N12: D3.cathode, J15.pin4
  N13: D4.cathode, J15.pin2
  N14: Q6.base, J12.pin3
  N15: Q6.collector, D6.anode
  N16: Q7.base, J12.pin4
  N17: Q7.collector, D5.anode
  N18: D5.cathode, J3.pin8
  N19: D6.cathode, J3.pin6
  N20: Q8.base, J12.pin1
  N21: Q8.collector, D8.anode
  N22: Q9.base, J12.pin2
  N23: Q9.collector, D7.anode
  N24: D7.cathode, J3.pin4
  N25: D8.cathode, J3.pin2
  N26: J13.pin1, Q14.base
  N27: J13.pin2, Q11.base
  N28: J13.pin3, Q15.base
  N29: J13.pin4, Q13.base
  N30: J14.pin1, Q16.base
  N31: J14.pin2, Q17.base
  N32: J14.pin3, Q12.base
  N33: J14.pin4, Q10.base
  N34: J3.pin1, J3.pin3, J3.pin5, J3.pin7, J15.pin1, J15.pin3, J15.pin5, J15.pin7, J16.pin1, J16.pin3, J16.pin5, J16.pin7, J17.pin1, J17.pin3, J17.pin5, J17.pin7, J18.pin1
  N35: Q10.collector, D13.anode
  N36: Q11.collector, D16.anode
  N37: Q12.collector, D9.anode
  N38: Q13.collector, D11.anode
  N39: Q14.collector, D15.anode
  N40: Q15.collector, D14.anode
  N41: Q16.collector, D10.anode
  N42: Q17.collector, D12.anode
  N43: D9.cathode, J17.pin6
  N44: D10.cathode, J17.pin2
  N45: D11.cathode, J16.pin8
  N46: D12.cathode, J17.pin4
  N47: D13.cathode, J17.pin8
  N48: D14.cathode, J16.pin6
  N49: D15.cathode, J16.pin2
  N50: D16.cathode, J16.pin4
