# Fritzing sketch id3_123456_0 (saved by Fritzing 0.9.3b)
breadboards: 1

parts:
  元件1 = Arduino Uno (Rev3)
  元件2 = Bluetooth HC-05 Macho
  hc-sr1 = hc-sr04
  hc-sr2 = hc-sr04
  U1 = TMP36 [package=to-92]
  元件3 = Monster Moto Shield

nets:
  N1: 元件1.D8, 元件3.OUTA1
  N2: 元件1.D9_PWM, 元件3.OUTB1
  N3: 元件1.D10_PWM/SS, 元件3.OUTA2
  N4: 元件1.D11_PWM/MOSI, 元件3.OUTB2
  N5: 元件1.D12/MISO, hc-sr1.Echo
  N6: 元件1.D13/SCK, hc-sr1.Trig
  N7: 元件1.D2, U1.VOUT
  N8: 元件1.D4, hc-sr2.Echo
  N9: 元件1.D5_PWM, hc-sr2.Trig
  N10: 元件1.D6_PWM, 元件2.RXD
  N11: 元件1.D7, 元件2.TXD
