# Fritzing sketch id4000_Synth_Guitar_0 (saved by Fritzing 0.9.2b)
circuit board: 14.0554cm x 9.85385cm
breadboards: 1

parts:
  R3 = Trimmer Potentiometer [maximum_resistance=100k package=THT]
  R4 = Trimmer Potentiometer [maximum_resistance=100k package=THT]
  R5 = Trimmer Potentiometer [maximum_resistance=100k package=THT]
  R6 = Trimmer Potentiometer [maximum_resistance=100k package=THT]
  R7 = Trimmer Potentiometer [maximum_resistance=100k package=THT]
  R8 = Trimmer Potentiometer [maximum_resistance=100k package=THT]
  R9 = Trimmer Potentiometer [maximum_resistance=100k package=THT]
  R10 = Trimmer Potentiometer [maximum_resistance=100k package=THT]
  S1 = Pushbutton [package="[THT]"]
  S2 = Pushbutton [package="[THT]"]
  S3 = Pushbutton [package="[THT]"]
  S4 = Pushbutton [package="[THT]"]
  S5 = Pushbutton [package="[THT]"]
  S6 = Pushbutton [package="[THT]"]
  S7 = Pushbutton [package="[THT]"]
  S8 = Pushbutton [package="[THT]"]
  VCC1 = Battery block 9V
  R5_2 = Resistor [tolerance=±5% resistance=100k package=THT]
  R4_2 = Resistor [tolerance=±5% resistance=100k package=THT]
  R1 = Resistor [tolerance=±5% resistance=47k package=THT]
  R2 = Resistor [tolerance=±5% resistance=22k package=THT]
  R3_2 = Resistor [tolerance=±5% resistance=10k package=THT]
  U1 = LM 358 Dual Op-Amp [package="DIP8 [THT]"]
  C1 = Ceramic Capacitor [capacitance=0.22mF package="100 mil [THT, multilayer]"]
  U3 = LM 358 Dual Op-Amp [package="DIP8 [THT]"]
  R11 = Resistor [tolerance=±5% resistance=22k package=THT]
  U2 = LM 358 Dual Op-Amp [package="DIP8 [THT]"]
  R12 = Resistor [tolerance=±5% resistance=100k package=THT]
  C2 = Electrolytic Capacitor [capacitance=2.2µF package="100 mil [THT, electrolytic]"]
  R8_2 = Resistor [tolerance=±5% resistance=470k package=THT]
  R6_2 = Resistor [tolerance=±5% resistance=47k package=THT]
  R7_2 = Resistor [tolerance=±5% resistance=22k package=THT]
  R9_2 = Resistor [tolerance=±5% resistance=100k package=THT]
  R10_2 = Resistor [tolerance=±5% resistance=100k package=THT]
  U4 = LM 358 Dual Op-Amp [package="DIP8 [THT]"]
  R14 = Resistor [tolerance=±5% resistance=47k package=THT]
  R15 = Resistor [tolerance=±5% resistance=4.7k package=THT]
  C3 = Electrolytic Capacitor [capacitance=4.7µF package="100 mil [THT, electrolytic]"]
  R31 = Resistor [tolerance=±5% resistance=470k package=THT]
  R29 = Resistor [tolerance=±5% resistance=390k package=THT]
  C4 = Ceramic Capacitor [capacitance=1nF package="100 mil [THT, multilayer]"]
  R28 = Resistor [tolerance=±5% resistance=22k package=THT]
  R24 = Resistor [tolerance=±5% resistance=10k package=THT]
  R26 = Resistor [tolerance=±5% resistance=100k package=THT]
  R27 = Resistor [tolerance=±5% resistance=100k package=THT]
  U5 = LM 358 Dual Op-Amp [package="DIP8 [THT]"]
  LDR2 = Photocell (LDR) [package=THT]
  R25 = Resistor [tolerance=±5% resistance=10k package=THT]
  LDR1 = Photocell (LDR) [package=THT]
  C5 = Ceramic Capacitor [capacitance=1nF package="100 mil [THT, multilayer]"]
  R30 = Resistor [tolerance=±5% resistance=22k package=THT]
  R32 = Resistor [tolerance=±5% resistance=10k package=THT]
  R33 = Resistor [tolerance=±5% resistance=22k package=THT]
  C6 = Electrolytic Capacitor [capacitance=4.7µF package="100 mil [THT, electrolytic]"]
  SPKR1 = Loudspeaker
  R13 = Rotary Potentiometer (Large) [maximum_resistance=100kΩ package=THT]

nets:
  N1: R3.wiper, S1.Pin_3, S1.Pin_4
  N2: R3.leg2, R4.leg2, R5.leg2, R7.leg2, R8.leg2, R9.leg2, R10.leg2, R3_2.Pin_1
  N3: R4.wiper, S2.Pin_3
  N4: R5.wiper, S3.Pin_3, S3.Pin_4
  N5: R6.wiper, S4.Pin_3, S4.Pin_4
  N6: R7.wiper, S5.Pin_3
  N7: R8.wiper, S6.Pin_3
  N8: R9.wiper, S7.Pin_3, S7.Pin_4
  N9: R10.wiper, S8.Pin_3, S8.Pin_4
  N10: S1.Pin_1, S1.Pin_2, S2.Pin_1, S2.Pin_2, S3.Pin_1, S3.Pin_2, S4.Pin_1, S4.Pin_2, S5.Pin_1, S5.Pin_2, S6.Pin_1, S6.Pin_2, S7.Pin_1, S7.Pin_2, S8.Pin_1, S8.Pin_2, R1.Pin_1, U1.connector0
  N11: VCC1.-, R5_2.Pin_0, U1.connector3, U3.connector3, U2.connector3, R10_2.Pin_0, U4.connector3, R15.Pin_0, R27.Pin_1, U5.connector3, R33.Pin_1, SPKR1.pin1, R13.leg1
  N12: VCC1.+, R4_2.Pin_1, U1.connector7, U3.connector7, U2.connector7, R9_2.Pin_0, U4.connector7, R26.Pin_0, U5.connector7, R13.leg2
  N13: R5_2.Pin_1, R4_2.Pin_0, U1.connector1, U1.connector4
  N14: R1.Pin_0, R2.Pin_1, U1.connector2
  N15: R2.Pin_0, U1.connector5, C1.0, U3.connector1
  N16: R3_2.Pin_0, U1.connector6, C1.1
  N17: U3.connector0, R14.Pin_1
  N18: U3.connector2, U3.connector6, R11.Pin_1
  N19: U3.connector4, R13.wiper
  N20: U3.connector5, R11.Pin_0, R12.Pin_1
  N21: U2.connector0, R8_2.Pin_0, R6_2.Pin_0
  N22: U2.connector1, U2.connector4
  N23: U2.connector2, R6_2.Pin_1, R7_2.Pin_0
  N24: U2.connector5, C2.+, R8_2.Pin_1
  N25: U2.connector6, R12.Pin_0, C2.-, R7_2.Pin_1
  N26: R9_2.Pin_1, R10_2.Pin_1
  N27: U4.connector0, R29.Pin_1, C4.1, LDR2.pin_0
  N28: U4.connector1, C4.0, R24.Pin_1
  N29: U4.connector2, R26.Pin_1, R27.Pin_0, U5.connector2
  N30: U4.connector4, R31.Pin_1, R29.Pin_0
  N31: U4.connector5, R28.Pin_1, R30.Pin_0
  N32: U4.connector6, R28.Pin_0, LDR1.pin_1
  N33: R14.Pin_0, R15.Pin_1, C3.+
  N34: C3.-, R31.Pin_0
  N35: R24.Pin_0, LDR1.pin_0
  N36: U5.connector0, C5.0, R30.Pin_1, R32.Pin_0
  N37: U5.connector1, R25.Pin_1, C5.1
  N38: LDR2.pin_1, R25.Pin_0
  N39: R32.Pin_1, R33.Pin_0, C6.+
  N40: C6.-, SPKR1.pin2
