# Fritzing sketch id4001_tabletop_0 (saved by Fritzing 0.9.3b)
breadboards: 1

parts:
  Part1 = Arduino Uno (Rev3)
  left_servo = Basic Servo
  left_micro-servo = Basic Servo
  right_micro-servo = Basic Servo
  right_servo = Basic Servo
  right_infrared_sensor = Infrared Proximity Sensor
  hc-sr1 = hc-sr04
  left_infrared_sensor = Infrared Proximity Sensor

nets:
  N1: Part1.A0, right_infrared_sensor.Vout
  N2: Part1.A1, left_infrared_sensor.Vout
  N3: Part1.D9_PWM, right_servo.pulse
  N4: Part1.D10_PWM/SS, left_servo.pulse
  N5: Part1.D2, hc-sr1.Trig
  N6: Part1.D3_PWM, hc-sr1.Echo
  N7: Part1.D5_PWM, right_micro-servo.pulse
  N8: Part1.D6_PWM, left_micro-servo.pulse
  VCC: Part1.5V, left_servo.vcc, left_micro-servo.vcc, right_micro-servo.vcc, right_servo.vcc, right_infrared_sensor.Vcc, hc-sr1.VCC, left_infrared_sensor.Vcc
  GND: Part1.GND, left_servo.gnd, left_micro-servo.gnd, right_micro-servo.gnd, right_servo.gnd, right_infrared_sensor.GND, hc-sr1.GND, left_infrared_sensor.GND
