# Fritzing sketch id4002_TactTone_0 (saved by Fritzing 0.7.12b)
breadboards: 1

parts:
  Arduino1 = Arduino
  S1 = Pushbutton [package="[THT]"]  # not connected
  S2 = Pushbutton [package="[THT]"]
  S3 = Pushbutton [package="[THT]"]
  S4 = Pushbutton [package="[THT]"]
  S5 = Pushbutton [package="[THT]"]
  S6 = Pushbutton [package="[THT]"]
  S7 = Pushbutton [package="[THT]"]
  S8 = Pushbutton [package="[THT]"]
  S9 = Pushbutton [package="[THT]"]
  S10 = Pushbutton [package="[THT]"]
  S11 = Pushbutton [package="[THT]"]
  S12 = Pushbutton [package="[THT]"]
  S13 = Pushbutton [package="[THT]"]
  S14 = Pushbutton [package="[THT]"]
  S15 = Toggle Switch [package=THT]
  LED1 = LED - 3mm [color="Green (570nm)" package="3 mm [THT]"]
  R1 = Resistor [tolerance=±5% resistance=10k package=THT]
  J1 = female pin header, 4 pins [form="♀ (female)"]
  R2 = Resistor [tolerance=±5% resistance=10k package=THT]
  R3 = Resistor [tolerance=±5% resistance=10k package=THT]
  R4 = Resistor [tolerance=±5% resistance=10k package=THT]
  R5 = Resistor [tolerance=±5% resistance=10k package=THT]
  R6 = Resistor [tolerance=±5% resistance=10k package=THT]
  R7 = Resistor [tolerance=±5% resistance=10k package=THT]
  R8 = Resistor [tolerance=±5% resistance=10k package=THT]
  R9 = Resistor [tolerance=±5% resistance=10k package=THT]
  R10 = Resistor [tolerance=±5% resistance=10k package=THT]
  R11 = Resistor [tolerance=±5% resistance=10k package=THT]
  R12 = Resistor [tolerance=±5% resistance=10k package=THT]
  R13 = Resistor [tolerance=±5% resistance=10k package=THT]
  R14 = Resistor [tolerance=±5% resistance=10k package=THT]
  R15 = Resistor [tolerance=±5% resistance=10k package=THT]
  J2 = female pin header, 4 pins [form="♀ (female)"]
  J3 = female pin header, 4 pins [form="♀ (female)"]
  J4 = female pin header, 4 pins [form="♀ (female)"]
  J5 = female pin header, 4 pins [form="♀ (female)"]
  J6 = female pin header, 2 pins [form="♀ (female)"]  # not connected
  LED2 = LED - 3mm [color="Green (570nm)" package="3 mm [THT]"]
  LED3 = LED - 3mm [color="Green (570nm)" package="3 mm [THT]"]
  LED4 = LED - 3mm [color="Green (570nm)" package="3 mm [THT]"]
  LED5 = LED - 3mm [color="Green (570nm)" package="3 mm [THT]"]
  LED6 = LED - 3mm [color="Green (570nm)" package="3 mm [THT]"]
  LED7 = LED - 3mm [color="Green (570nm)" package="3 mm [THT]"]
  LED8 = LED - 3mm [color="Green (570nm)" package="3 mm [THT]"]
  LED9 = LED - 3mm [color="Red (660nm)" package="3 mm [THT]"]
  LED10 = LED - 3mm [color="Red (660nm)" package="3 mm [THT]"]
  LED11 = LED - 3mm [color="Red (660nm)" package="3 mm [THT]"]
  LED12 = LED - 3mm [color="Red (660nm)" package="3 mm [THT]"]
  LED13 = LED - 3mm [color="Red (660nm)" package="3 mm [THT]"]
  LED14 = LED - 3mm [color="Red (660nm)" package="3 mm [THT]"]
  J7 = Piezo Speaker

nets:
  N1: Arduino1.D12, S15.L1, S15.COM, S15.L2, R11.Pin_1, J4.pin1
  N2: Arduino1.D11, J2.pin1, J5.pin1, J7.pin2
  N3: Arduino1.D9, S11.Pin_3, S11.Pin_4, R5.Pin_1, J2.pin4, LED11.cathode, LED11.anode
  N4: Arduino1.D8, R15.Pin_1, J3.pin1, LED5.cathode, LED5.anode
  N5: Arduino1.D7, S12.Pin_1, S12.Pin_2, R14.Pin_1, J3.pin2, LED12.cathode, LED12.anode
  N6: Arduino1.D6, R13.Pin_1, J3.pin3, LED6.cathode, LED6.anode
  N7: Arduino1.D5, S13.Pin_3, S13.Pin_4, R12.Pin_1, J3.pin4, LED13.cathode, LED13.anode
  N8: Arduino1.D4, R10.Pin_1, J4.pin2, LED7.cathode, LED7.anode
  N9: Arduino1.D3, R9.Pin_1, J4.pin3, LED8.cathode, LED8.anode
  N10: Arduino1.D2, S14.Pin_3, S14.Pin_4, R8.Pin_1, J4.pin4, LED14.cathode, LED14.anode
  N11: Arduino1.GND, J7.pin1
  N12: Arduino1.A0, S2.Pin_3, S2.Pin_4, LED1.cathode, LED1.anode, R1.Pin_1, J1.pin1
  N13: Arduino1.A1, J1.pin2, R2.Pin_1, LED9.cathode, LED9.anode
  N14: Arduino1.A2, S2.Pin_1, S2.Pin_2, J1.pin3, R3.Pin_1, LED2.cathode, LED2.anode
  N15: Arduino1.A3, J1.pin4, R4.Pin_1, LED10.cathode, LED10.anode
  N16: Arduino1.A4, R7.Pin_1, J2.pin2, LED3.cathode, LED3.anode
  N17: Arduino1.A5, R6.Pin_1, J2.pin3, LED4.cathode, LED4.anode
  N18: S3.Pin_1, S3.Pin_2
  N19: S3.Pin_3, S3.Pin_4
  N20: S4.Pin_1, S4.Pin_2
  N21: S4.Pin_3, S4.Pin_4
  N22: S5.Pin_1, S5.Pin_2
  N23: S5.Pin_3, S5.Pin_4
  N24: S6.Pin_1, S6.Pin_2
  N25: S6.Pin_3, S6.Pin_4
  N26: S7.Pin_1, S7.Pin_2
  N27: S7.Pin_3, S7.Pin_4
  N28: S8.Pin_1, S8.Pin_2
  N29: S8.Pin_3, S8.Pin_4
  N30: S9.Pin_1, S9.Pin_2
  N31: S9.Pin_3, S9.Pin_4
  N32: S10.Pin_1, S10.Pin_2
  N33: S10.Pin_3, S10.Pin_4
  N34: S11.Pin_1, S11.Pin_2
  N35: S12.Pin_3, S12.Pin_4
  N36: S13.Pin_1, S13.Pin_2
  N37: S14.Pin_1, S14.Pin_2
