# Fritzing sketch id4003_Horloge_Parlante_LCD_Mise_a_L_heure_0 (saved by Fritzing 0.9.3b)
breadboards: 1

parts:
  Composant1 = Arduino Nano (Rev3.0)
  DFPlayer_Mini1 = DFPlayer Mini
  ZS-042_RTC1 = ZS-042 RTC Module
  U1 = LCD-16X2 [package=lcd-16x2_noholes]
  R1 = Resistor [tolerance=±5% resistance=1k package=THT]
  SP1 = SPEAKER [package=pcb_mount_speaker]
  S1 = Pushbutton [package="[SMD]"]
  S2 = Pushbutton [package="[SMD]"]
  S3 = Pushbutton [package="[SMD]"]
  S4 = Pushbutton [package="[SMD]"]
  S5 = Pushbutton [package="[SMD]"]
  R3 = Resistor [tolerance=±5% resistance=1k package=THT]
  R4 = Resistor [tolerance=±5% resistance=1k package=THT]
  R5 = Resistor [tolerance=±5% resistance=1k package=THT]
  R6 = Resistor [tolerance=±5% resistance=1k package=THT]
  R7 = Resistor [tolerance=±5% resistance=1k package=THT]

nets:
  N1: Composant1.D1/TX, R1.Pin_0
  N2: Composant1.D2, U1.K
  N3: Composant1.D3, U1.A
  N4: Composant1.D4, U1.DB7
  N5: Composant1.D5, U1.DB6
  N6: Composant1.D6, S5.Pin_3, S5.Pin_4, R7.Pin_0
  N7: Composant1.D7, S1.Pin_3, R3.Pin_0
  N8: Composant1.D8, S2.Pin_3, S2.Pin_4, R4.Pin_0
  N9: Composant1.D9, S3.Pin_3, S3.Pin_4, R5.Pin_0
  N10: Composant1.D10, S4.Pin_3, S4.Pin_4, R6.Pin_0
  N11: Composant1.D11/MOSI, U1.E
  N12: Composant1.D12/MISO, U1.RS
  N13: Composant1.A5, ZS-042_RTC1.SCL
  N14: Composant1.A4, ZS-042_RTC1.SDA
  VCC: DFPlayer_Mini1.connector0, ZS-042_RTC1.VCC, U1.VDD, S5.Pin_2
  N15: DFPlayer_Mini1.connector1, R1.Pin_1
  N16: DFPlayer_Mini1.connector5, SP1.-
  GND: DFPlayer_Mini1.connector6, ZS-042_RTC1.GND, U1.VSS, U1.VO, U1.R_W, R7.Pin_1
  N17: DFPlayer_Mini1.connector7, SP1.+
