# Fritzing sketch id4003_Semaforo_por_Demanda_PULSADOR_peaton_Ferreyra_Nidia (saved by Fritzing 0.9.3b)
breadboards: 1

parts:
  Componente1 = Arduino Uno (Rev3)
  R1 = Resistor [tolerance=±5% resistance=10k package=THT]
  R2 = Resistor [tolerance=±5% resistance=220 package=THT]
  R3 = Resistor [tolerance=±5% resistance=220 package=THT]
  R4 = Resistor [tolerance=±5% resistance=220 package=THT]
  S1 = Momentary Switch [package=ksa_sealed_tac_switch]
  LED2 = LED - 3mm [color="Yellow (595nm)" package="3 mm [THT]"]
  LED1 = LED - 3mm [color="Green (560nm)" package="3 mm [THT]"]
  LED3 = LED - 3mm [color="Red (633nm)" package="3 mm [THT]"]

nets:
  N1: Componente1.GND, R1.Pin_1, LED2.cathode, LED3.cathode
  N2: Componente1.D2, R1.Pin_0, S1.3
  N3: Componente1.D5_PWM, R2.Pin_0
  N4: Componente1.D6_PWM, R3.Pin_0
  N5: Componente1.D7, R4.Pin_1
  N6: Componente1.5V, S1.2
  N7: R2.Pin_1, LED3.anode
  N8: R3.Pin_1, LED2.anode
  N9: R4.Pin_0, LED1.anode
