# Fritzing sketch id4004_AnalogReadSerial2LCD_LEDBLUETOOTH_0 (saved by Fritzing 0.9.3b)
circuit board: 8.46667cm x 5.64444cm
breadboards: 1

parts:
  Onderdeel1 = Arduino Uno (Rev3)
  LCM1602_IIC1 = generic_ic_dip_22_300mil.fzp [part_number="LCM1602 IIC" chip_label="LCM1602 IIC"]
  LCD1 = LCD screen
  Parte3 = HC-SR04 ultrasonic distance sensor
  LED1 = LED - 5mm [color="Red (633nm)" package="5 mm [THT]"]
  R1 = Resistor [tolerance=±5% resistance=220 package=THT]
  R2 = Resistor [tolerance=±5% resistance=220 package=THT]
  LED3 = LED - 5mm [color="Red (633nm)" package="5 mm [THT]"]
  Parte7 = bluetooth-module

nets:
  N1: Onderdeel1.A4/SDA, LCM1602_IIC1.connector18
  N2: Onderdeel1.A5/SCL, LCM1602_IIC1.connector19
  N3: Onderdeel1.D11_PWM/MOSI, LED1.cathode
  N4: Onderdeel1.D12/MISO, LED3.cathode
  N5: Onderdeel1.GND, LCM1602_IIC1.connector16, Parte3.connector3, R1.Pin_0, R2.Pin_0, Parte7.connector14
  N6: Onderdeel1.D0/RX, Parte7.connector15
  N7: Onderdeel1.D1/TX, Parte7.connector16
  N8: Onderdeel1.D2, Parte3.connector2
  N9: Onderdeel1.D3_PWM, Parte3.connector1
  N10: Onderdeel1.5V, LCM1602_IIC1.connector17, Parte3.connector0, Parte7.connector13
  N11: LCM1602_IIC1.connector0, LCD1.VSS
  N12: LCM1602_IIC1.connector1, LCD1.VDD
  N13: LCM1602_IIC1.connector2, LCD1.V0
  N14: LCM1602_IIC1.connector3, LCD1.RS
  N15: LCM1602_IIC1.connector4, LCD1.R/W
  N16: LCM1602_IIC1.connector5, LCD1.E
  N17: LCM1602_IIC1.connector6, LCD1.DB0
  N18: LCM1602_IIC1.connector7, LCD1.DB1
  N19: LCM1602_IIC1.connector8, LCD1.DB2
  N20: LCM1602_IIC1.connector9, LCD1.DB3
  N21: LCM1602_IIC1.connector10, LCD1.DB4
  N22: LCM1602_IIC1.connector11, LCD1.DB5
  N23: LCM1602_IIC1.connector12, LCD1.DB6
  N24: LCM1602_IIC1.connector13, LCD1.DB7
  N25: LCM1602_IIC1.connector14, LCD1.LED+
  N26: LCM1602_IIC1.connector15, LCD1.LED-
  N27: LCM1602_IIC1.connector20, LCM1602_IIC1.connector21
  N28: LED1.anode, R2.Pin_1
  N29: R1.Pin_1, LED3.anode
