# Fritzing sketch id4005_tandberg_motors_0 (saved by Fritzing 0.9.2b)
breadboards: 1

parts:
  Part1 = Arduino Leonardo (Rev3b)
  Raspberry_Pi1 = Raspberry Pi B rev2  # not connected
  M1 = DC Motor
  BAT1 = BC9VPC [package=bc9vpc]
  Q1 = Basic FET N-Channel [package="TO220 [THT]"]
  U1 = RELAY [package=relay-t9a]
  U2 = RELAY [package=relay-t9a]
  R1 = Resistor [tolerance=±5% resistance=1k package="0603 [SMD]"]

nets:
  N1: Part1.D2/SDA, U1.COIL1
  N2: Part1.D3_PWM/SCL, U2.COIL1
  N3: Part1.D5_PWM, Q1.gate, R1.Pin_0
  N4: Part1.GND, BAT1.V-, Q1.source, U1.COIL2, U2.COIL2, R1.Pin_1
  N5: M1.pin_1, U1.MAIN
  N6: M1.pin_2, U2.MAIN
  N7: BAT1.V+, U1.NO, U2.NO
  N8: Q1.drain, U1.NC, U2.NC
