# Fritzing sketch id4006_tapsync_0 (saved by Fritzing 0.9.3b)
breadboards: 1

parts:
  Part1 = Arduino Nano (Rev3.0)
  R1 = Resistor [tolerance=±5% resistance=220 package=THT]
  R3 = Resistor [tolerance=±5% resistance=220 package=THT]
  D1 = Rectifier Diode [part_number=1N4001 package="300 mil [THT]"]
  TRS1 = Audio Jack (TRS) 3.5mm [package="PG203J [THT]"]
  J1 = Power Jack [package=power_jack_combo]
  LED1 = LED - 3mm [color="Red (633nm)" package="3 mm [THT]"]
  R4 = Resistor [tolerance=±5% resistance=220 package=THT]
  S1 = SWITCH-MOMENTARY-2 [package=tactile-pth-12mm]
  R5 = Resistor [tolerance=±5% resistance=4.7k package=THT]

nets:
  N1: Part1.D1/TX, R1.Pin_0
  GND: Part1.GND, TRS1.Sleeve, J1.GND, LED1.cathode, S1.2
  N2: Part1.D2, S1.1, R5.Pin_1
  N3: Part1.D3, R4.Pin_0
  N4: Part1.VIN, D1.cathode
  N5: Part1.5V, R5.Pin_0
  N6: Part1.3V3, R3.Pin_0
  N7: R1.Pin_1, TRS1.Tip
  N8: R3.Pin_1, TRS1.Ring
  N9: D1.anode, J1.PWR
  N10: LED1.anode, R4.Pin_1
