# Fritzing sketch id4007_TAP&TALK_0 (saved by Fritzing 0.9.3b)
breadboards: 1

parts:
  Teensy_3_1 = Teensy 3.1  # not connected
  Part1 = Bluetooth HC-05 Macho
  U7 = SWITCH-SPST-2 [package=r_sw_th]
  S7 = Round Pushbutton
  S8 = Round Pushbutton
  S9 = Round Pushbutton
  S10 = Round Pushbutton
  S11 = Round Pushbutton
  S12 = Round Pushbutton
  U8 = SWITCH-SPST-2 [package=r_sw_th]
  U9 = SWITCH-SPST-2 [package=r_sw_th]
  U10 = SWITCH-SPST-2 [package=r_sw_th]
  U11 = SWITCH-SPST-2 [package=r_sw_th]
  U12 = SWITCH-SPST-2 [package=r_sw_th]
  U13 = Vibration Motor- ROB-08449 [package=vibe-motor-10mm]
  VCC2 = Battery block 9V
  U14 = Vibration Motor- ROB-08449 [package=vibe-motor-10mm]
  U15 = Vibration Motor- ROB-08449 [package=vibe-motor-10mm]
  U16 = Vibration Motor- ROB-08449 [package=vibe-motor-10mm]
  U17 = Vibration Motor- ROB-08449 [package=vibe-motor-10mm]
  U18 = Vibration Motor- ROB-08449 [package=vibe-motor-10mm]
  U19 = Vibration Motor- ROB-08449 [package=vibe-motor-10mm]
  S13 = Round Pushbutton
  U20 = SWITCH-SPST-2 [package=r_sw_th]

nets:
  N1: Part1.VCC, VCC2.+
  N2: Part1.GND, VCC2.-, U14.-, S13.leg0, U20.O
  N3: U7.O, S7.leg0, S8.leg0, S9.leg0, S10.leg0, S11.leg0, S12.leg0, U8.O, U9.O, U10.O, U10.P, U11.O, U11.P, U12.O, U12.P, U13.-, U15.-, U16.-, U17.-, U18.-, U19.-
