# Fritzing sketch id4008_tarea_0 (saved by Fritzing 0.9.3b)
breadboards: 1

parts:
  Componente1 = Arduino Uno (Rev3)
  R1 = Resistor [tolerance=±5% resistance=220 package=THT]
  LED1 = LED - 5mm [color="Green (570nm)" package="5 mm [THT]"]
  LED3 = LED - 5mm [color="Red (633nm)" package="5 mm [THT]"]
  J1 = Piezo Speaker
  Parte3 = HC-SR04 ultrasonic distance sensor
  R2 = Resistor [tolerance=±5% resistance=220 package=THT]

nets:
  N1: Componente1.D8, Componente1.D7, Componente1.5V, LED1.cathode, LED3.cathode, J1.pin1
  N2: Componente1.D10_PWM/SS, R2.Pin_1
  N3: Componente1.D11_PWM/MOSI, R1.Pin_1
  N4: Componente1.D5_PWM, J1.pin2
  N5: R1.Pin_0, LED1.anode
  N6: LED3.anode, R2.Pin_0
  N7: Parte3.connector0, Parte3.connector1, Parte3.connector2, Parte3.connector3
