# Fritzing sketch id4009_Tarefa_analogRead_0 (saved by Fritzing 0.9.3b)
breadboards: 1

parts:
  R2 = Trimmer Potentiometer [maximum_resistance=10kΩ package=THT]
  Componente1 = Arduino Uno (Rev3)

nets:
  N1: R2.leg1, Componente1.GND
  N2: R2.wiper, Componente1.A0
  N3: R2.leg2, Componente1.5V
