# Fritzing sketch id4010_hola_buenas_0 (saved by Fritzing 0.9.3b)
breadboards: 1

parts:
  Componente1 = Arduino Uno (Rev3)
  R2 = TRIMPOT [package=trimpot-3mm]

nets:
  N1: Componente1.A0, R2.WIPER
  N2: Componente1.5V, R2.CCW
  N3: Componente1.GND, R2.CW
