# Fritzing sketch id4011_ROBOT_ACUATICO_0 (saved by Fritzing 0.9.2b)
circuit board: 3.5cm x 3.3cm
breadboards: 1

parts:
  Q1 = NPN-Transistor [package="TO92 [THT]"]
  Q2 = NPN-Transistor [package="TO92 [THT]"]
  R1 = Resistor [tolerance=±5% resistance=330 package=THT]
  R2 = Resistor [tolerance=±5% resistance=330 package=THT]
  D1 = Rectifier Diode [part_number=1N4007 package="300 mil [THT]"]
  D2 = Rectifier Diode [part_number=1N4007 package="300 mil [THT]"]
  R3 = Resistor [tolerance=±5% resistance=1k package=THT]
  R4 = Resistor [tolerance=±5% resistance=1k package=THT]
  J1 = female pin header, 2 pins [form="♀ (female)"]
  J2 = female pin header, 2 pins [form="♀ (female)"]
  J3 = female pin header, 5 pins [form="♀ (female)"]
  J4 = female pin header, 2 pins [form="♀ (female)"]
  J5 = female pin header, 2 pins [form="♀ (female)"]
  J6 = female pin header, 2 pins [form="♀ (female)"]
  J7 = female pin header, 5 pins [form="♀ (female)"]

nets:
  N1: Q1.E, Q2.E, J3.pin1, J3.pin2, J3.pin3, J3.pin4, J3.pin5
  N2: Q1.B, R3.Pin_1
  N3: Q1.C, D1.anode, J1.pin1, J2.pin1
  N4: Q2.B, R4.Pin_1
  N5: Q2.C, D2.anode, J5.pin1, J6.pin1
  N6: R1.Pin_0, J1.pin2
  N7: R1.Pin_1, R2.Pin_1, D1.cathode, D2.cathode, J2.pin2, J6.pin2, J7.pin1, J7.pin2, J7.pin3, J7.pin4, J7.pin5
  N8: R2.Pin_0, J5.pin2
  N9: R3.Pin_0, J4.pin1
  N10: R4.Pin_0, J4.pin2

notes:
  CLUB ROBOTICA TACNA
