# Fritzing sketch id4012_Tarjeta_Presentacion_V1_0 (saved by Fritzing 0.9.3b)
circuit board: 8.55cm x 5.4cm
breadboards: 1

parts:
  Atmega328P = atmega328 [package=dip]
  10K = Resistor [tolerance=±5% resistance=220 package=THT]
  +5V = Battery
  part = LED - 3mm [color="Red (633nm)" package="3 mm [THT]"]
  XL = CRYSTAL - kHz [frequency="16 Mhz"]
  22p = Capacitor [package=cap-pth-small-kit]
  22p_2 = Capacitor [package=cap-pth-small-kit]
  -_+ = Rectifier Diode [part_number=1N4001 package="300 mil [THT]"]
  RGB = RGB LED - (4 legs) [package="5 mm [THT]"]
  1K = Resistor [tolerance=±5% resistance=220 package=THT]
  0_1u = Ceramic Capacitor [capacitance=100nF package="100 mil [THT, multilayer]"]
  1K_2 = Resistor [tolerance=±5% resistance=220 package=THT]
  part_2 = LED - 3mm [color="Red (633nm)" package="3 mm [THT]"]
  LDR = Capacitor [package=cap-pth-small-kit]
  100k = Resistor [tolerance=±5% resistance=220 package=THT]
  USB = USB+SHIELD [package=usb-b-pth]
  + = Rectifier Diode [part_number=1N4001 package="300 mil [THT]"]

nets:
  N1: Atmega328P.RESET, 10K.Pin_1, 0_1u.0
  N2: Atmega328P.VCC, Atmega328P.AVCC, Atmega328P.AREF, 10K.Pin_0, -_+.cathode, part_2.anode, 100k.Pin_0, +.cathode
  GND: Atmega328P.GND, +5V.+, part.cathode, 22p.1, 22p_2.1, 1K_2.Pin_0, LDR.2, USB.GND
  N3: Atmega328P.XLAT1, XL.pin_0, 22p_2.2
  N4: Atmega328P.XLAT2, XL.pin_1, 22p.2
  N5: Atmega328P.D5_(PWM), RGB.blue_cathode
  N6: Atmega328P.D6_(PWM), RGB.green_cathode
  N7: Atmega328P.D7, RGB.red_cathode
  N8: +5V.-, -_+.anode, USB.VBUS
  N9: RGB.common_anode, 1K.Pin_0
  N10: 1K_2.Pin_1, part_2.cathode
  N11: LDR.1, 100k.Pin_1

notes:
  Videos de Robótica y Electrónica
  El Profe García
  -
  16Mhz
  facebook.com/elprofe.garcia
  youtube.com/elprofegarcia
  twitter.com/El_Profe_Garcia
  www.elprofegarcia.com
  A5 A4 A3 A2 A1 A0
  13 12 11´10´ 9´ 8
  RST 0  1  2  3´ 4  +  -
  5´ 6´ 7  8
  +5Vcc
  GND
  RX TX
  SCL
  SDA
  +5V GND TX RX
  Arduino UNO PRO-FE
  Bluetooth HC06
  7.6.5
  USB-Serial
  5V GND TX RX
  GND +V TX RX DTR
  .
  -----
  cc
  -1K-
  ----- Ardu5 -----
  instagram.com/el_profe_garcia
