# Fritzing sketch id4014_TBD_0 (saved by Fritzing 0.9.3b)

parts:
  Part1 = Arduino Ethernet Shield (Rev3)  # not connected
  Part2 = Arduino Uno (Rev3) - ICSP  # not connected
  Part3 = Bluetooth HC-05 Macho
  Part4 = Arduino Motor Shield (Rev3)
  M1 = DC Motor
  M2 = DC Motor
  M3 = DC Motor
  M4 = DC Motor

nets:
  N1: Part3.TXD, Part4.D1/TX
  N2: Part3.RXD, Part4.IOREF
  VCC: Part3.VCC, Part4.3V3
  GND: Part3.GND, Part4.GND
  N3: Part4.B-, M1.pin_2, M2.pin_2
  N4: Part4.B+, M1.pin_1, M2.pin_1
  N5: Part4.A-, M3.pin_1, M4.pin_1
  N6: Part4.A+, M3.pin_2, M4.pin_2
