# Fritzing sketch id4015_TBS_Core_v1.3_4_2fzz_0 (saved by Fritzing 0.9.0b)
circuit board: 3.6cm x 2.6cm
breadboards: 1

parts:
  D1 = Schottky Diode [part_number=1N5817 package="300 mil [THT]"]
  L1 = Inductor [package="400 mil [THT]"]
  vtx = female pin header, 5 pins [form="♀ (female)"]
  cam = female pin header, 12 pins [form="♀ (female)"]
  C3 = Electrolytic Capacitor [capacitance=22µF voltage=35V package="100 mil [THT, electrolytic]"]
  IC1 = LM_7940
  C2 = Ceramic Capacitor [capacitance=0.47µF voltage=50V package="100 mil [THT, multilayer]"]
  C1 = Electrolytic Capacitor [capacitance=470µF voltage=35V package="100 mil [THT, electrolytic]"]
  J1 = female pin header, 3 pins [form="♀ (female)"]
  J2 = female pin header, 3 pins [form="♀ (female)"]

nets:
  N1: D1.cathode, L1.pin_0
  N2: D1.anode, cam.pin5
  N3: L1.pin_1, IC1.connector0, C2.0, C1.+
  N4: vtx.pin1, cam.pin8, C3.+, IC1.connector2
  N5: vtx.pin2, cam.pin6, cam.pin9, C3.-, IC1.connector1, C2.1, C1.-, J1.pin2, J2.pin2
  N6: vtx.pin3, J1.pin3
  N7: cam.pin10, J2.pin3

notes:
  v+
  gnd
  video
  vin
  TBS 12V r1.0
  domepat
