# Fritzing sketch id4017_TCA_140211_r6_0 (saved by Fritzing 0.8.7b)
circuit board: 12cm x 8cm
breadboards: 1

parts:
  A_Micro_R3 = Arduino Micro (Rev3)
  Q1 = NPN-Transistor [package="TO92 [THT]"]
  Ry1 = HFD2 V2 0000
  R1 = Resistor [tolerance=±5% resistance=1k package=THT]
  R2 = Resistor [tolerance=±5% resistance=1k package=THT]
  R3 = Resistor [tolerance=±5% resistance=1k package=THT]
  Fu1 = prefix0000
  LED1 = LED - 3mm [color="Red (633nm)" package="3 mm [THT]"]
  D1 = Rectifier Diode [part_number=1N4148 package="300 mil [THT]"]
  J3 = male pin header, 4 pins [form="♂ (male)"]
  J4 = male pin header, 10 pins [form="♂ (male)"]
  J1 = male pin header, 2 pins [form="♂ (male)"]
  J2 = male pin header, 6 pins [form="♂ (male)"]
  R4 = Resistor [tolerance=±5% resistance=1k package=THT]
  R5 = Resistor [tolerance=±5% resistance=1k package=THT]
  R6 = Resistor [tolerance=±5% resistance=1k package=THT]
  Pw1 = prefix0000
  R7 = Resistor [tolerance=±5% resistance=1k package=THT]
  R8 = Resistor [tolerance=±5% resistance=1k package=THT]
  R9 = Resistor [tolerance=±5% resistance=1k package=THT]
  R10 = Resistor [tolerance=±5% resistance=1k package=THT]
  R11 = Resistor [tolerance=±5% resistance=1k package=THT]
  R12 = Resistor [tolerance=±5% resistance=1k package=THT]
  R13 = Resistor [tolerance=±5% resistance=1k package=THT]
  R14 = Resistor [tolerance=±5% resistance=1k package=THT]
  R15 = Resistor [tolerance=±5% resistance=1k package=THT]
  R16 = Resistor [tolerance=±5% resistance=1k package=THT]
  R17 = Resistor [tolerance=±5% resistance=1k package=THT]
  R18 = Resistor [tolerance=±5% resistance=1k package=THT]
  R19 = Resistor [tolerance=±5% resistance=10k package=THT]
  R20 = Resistor [tolerance=±5% resistance=10k package=THT]
  R21 = Resistor [tolerance=±5% resistance=10k package=THT]
  R22 = Resistor [tolerance=±5% resistance=10k package=THT]
  R23 = Resistor [tolerance=±5% resistance=10k package=THT]
  R24 = Resistor [tolerance=±5% resistance=10k package=THT]
  R25 = Resistor [tolerance=±5% resistance=1k package=THT]
  R26 = Resistor [tolerance=±5% resistance=1k package=THT]
  R27 = Resistor [tolerance=±5% resistance=1k package=THT]
  R28 = Resistor [tolerance=±5% resistance=1k package=THT]
  R29 = Resistor [tolerance=±5% resistance=1k package=THT]
  R30 = Resistor [tolerance=±5% resistance=1k package=THT]
  R31 = Resistor [tolerance=±5% resistance=1k package=THT]
  R32 = Resistor [tolerance=±5% resistance=1k package=THT]
  LED2 = LED - 3mm [color="Orange (612nm)" package="3 mm [THT]"]
  C3 = Ceramic Capacitor [capacitance=100nF voltage=35V package="200 mil [THT, multilayer]"]
  C2 = Ceramic Capacitor [capacitance=100nF voltage=35V package="200 mil [THT, multilayer]"]
  C1 = Electrolytic Capacitor [capacitance=68µF voltage=35V package="200 mil [THT, electrolytic]"]
  Q2 = NPN-Transistor [package="TO92 [THT]"]
  Q3 = NPN-Transistor [package="TO92 [THT]"]
  Q4 = NPN-Transistor [package="TO92 [THT]"]
  Q5 = NPN-Transistor [package="TO92 [THT]"]
  Q6 = NPN-Transistor [package="TO92 [THT]"]
  D2 = Rectifier Diode [part_number=1N4001 package="300 mil [THT]"]
  S1 = LED - 3mm [color="Red (633nm)" package="3 mm [THT]"]
  S2 = LED - 3mm [color="Red (633nm)" package="3 mm [THT]"]
  Ry2 = HFD2 V2 0000
  D3 = Rectifier Diode [part_number=1N4001 package="300 mil [THT]"]
  S3 = LED - 3mm [color="Red (633nm)" package="3 mm [THT]"]
  Ry3 = HFD2 V2 0000
  D4 = Rectifier Diode [part_number=1N4001 package="300 mil [THT]"]
  S4 = LED - 3mm [color="Red (633nm)" package="3 mm [THT]"]
  Ry4 = HFD2 V2 0000
  D5 = Rectifier Diode [part_number=1N4001 package="300 mil [THT]"]
  S5 = LED - 3mm [color="Red (633nm)" package="3 mm [THT]"]
  Ry5 = HFD2 V2 0000
  D6 = Rectifier Diode [part_number=1N4001 package="300 mil [THT]"]
  S6 = LED - 3mm [color="Red (633nm)" package="3 mm [THT]"]
  Ry6 = HFD2 V2 0000
  D7 = Rectifier Diode [part_number=1N4001 package="300 mil [THT]"]
  S1_2 = male pin header, 3 pins [form="♂ (male)"]
  S2_2 = male pin header, 3 pins [form="♂ (male)"]
  S3_2 = male pin header, 3 pins [form="♂ (male)"]
  S4_2 = male pin header, 3 pins [form="♂ (male)"]
  S5_2 = male pin header, 3 pins [form="♂ (male)"]
  S6_2 = male pin header, 3 pins [form="♂ (male)"]

nets:
  N1: A_Micro_R3.D1/TX, R13.Pin_0, R19.Pin_0
  GND: A_Micro_R3.GND, Q1.E, J4.pin2, Pw1.connector1, LED2.cathode, C3.0, C2.0, C1.-, Q2.E, Q3.E, Q4.E, Q5.E, Q6.E, S1.cathode, S2.cathode, S3.cathode, S4.cathode, S5.cathode, S6.cathode, S1_2.pin3, S2_2.pin3, S3_2.pin3, S4_2.pin3, S5_2.pin3, S6_2.pin3
  N2: A_Micro_R3.D2/SDA, R14.Pin_0, R20.Pin_0
  N3: A_Micro_R3.D3/SCL, R15.Pin_0, R21.Pin_0
  N4: A_Micro_R3.D4_PWM/A6, R16.Pin_0, R22.Pin_0
  N5: A_Micro_R3.D5_PWM, R17.Pin_0, R23.Pin_0
  N6: A_Micro_R3.D6_PWM/A7, R18.Pin_0, R24.Pin_0
  N7: A_Micro_R3.D7, R7.Pin_0
  N8: A_Micro_R3.D8_PWM/A8, R8.Pin_0
  N9: A_Micro_R3.D9_PWM/A9, R9.Pin_0
  N10: A_Micro_R3.D10_PWM/A10, R10.Pin_0
  N11: A_Micro_R3.D11_PWM, R11.Pin_0
  N12: A_Micro_R3.D12_PWM/A11, R12.Pin_0
  5V: A_Micro_R3.5V, Ry1.connector3, Ry1.connector15, Fu1.connector1, D1.cathode, C3.1, D2.cathode, Ry2.connector3, Ry2.connector15, D3.cathode, Ry3.connector3, Ry3.connector15, D4.cathode, Ry4.connector3, Ry4.connector15, D5.cathode, Ry5.connector3, Ry5.connector15, D6.cathode, Ry6.connector3, Ry6.connector15, D7.cathode, S1_2.pin1, S2_2.pin1, S3_2.pin1, S4_2.pin1, S5_2.pin1, S6_2.pin1
  N13: A_Micro_R3.A5, R6.Pin_1
  N14: A_Micro_R3.A4, R5.Pin_1
  N15: A_Micro_R3.A3, R4.Pin_1
  N16: A_Micro_R3.A2, R3.Pin_1
  N17: A_Micro_R3.A1, R2.Pin_1
  N18: A_Micro_R3.A0, R1.Pin_1
  N19: Q1.B, R19.Pin_1
  N20: Q1.C, Ry1.connector0, D2.anode
  N21: Ry1.connector7, R25.Pin_1
  TB: Ry1.connector8, J1.pin2, Ry2.connector8, Ry3.connector8, Ry4.connector8, Ry5.connector8, Ry6.connector8
  TA: Ry1.connector10, J1.pin1, Ry2.connector10, Ry3.connector10, Ry4.connector10, Ry5.connector10, Ry6.connector10
  F1: Ry1.connector12, J2.pin1
  A0: R1.Pin_0, J4.pin9
  A1: R2.Pin_0, J4.pin10
  N22: R3.Pin_0, J3.pin1
  N23: Fu1.connector0, Pw1.connector0, R31.Pin_0, R32.Pin_0, C2.1, C1.+
  N24: LED1.cathode, D1.anode
  N25: LED1.anode, R31.Pin_1
  N26: J3.pin2, R4.Pin_0
  N27: J3.pin3, R5.Pin_0
  N28: J3.pin4, R6.Pin_0
  N29: J4.pin3, R13.Pin_1
  N30: J4.pin4, R14.Pin_1
  N31: J4.pin5, R15.Pin_1
  N32: J4.pin6, R16.Pin_1
  N33: J4.pin7, R17.Pin_1
  N34: J4.pin8, R18.Pin_1
  F2: J2.pin2, Ry2.connector12
  F3: J2.pin3, Ry3.connector12
  F4: J2.pin4, Ry4.connector12
  F5: J2.pin5, Ry5.connector12
  F6: J2.pin6, Ry6.connector12
  S1: R7.Pin_1, S1_2.pin2
  S2: R8.Pin_1, S2_2.pin2
  S3: R9.Pin_1, S3_2.pin2
  S4: R10.Pin_1, S4_2.pin2
  S5: R11.Pin_1, S5_2.pin2
  S6: R12.Pin_1, S6_2.pin2
  N35: R20.Pin_1, Q2.B
  N36: R21.Pin_1, Q3.B
  N37: R22.Pin_1, Q4.B
  N38: R23.Pin_1, Q5.B
  N39: R24.Pin_1, Q6.B
  N40: R25.Pin_0, S1.anode
  N41: R26.Pin_0, S2.anode
  N42: R26.Pin_1, Ry2.connector7
  N43: R27.Pin_0, S3.anode
  N44: R27.Pin_1, Ry3.connector7
  N45: R28.Pin_0, S4.anode
  N46: R28.Pin_1, Ry4.connector7
  N47: R29.Pin_0, S5.anode
  N48: R29.Pin_1, Ry5.connector7
  N49: R30.Pin_0, S6.anode
  N50: R30.Pin_1, Ry6.connector7
  N51: R32.Pin_1, LED2.anode
  N52: Q2.C, Ry2.connector0, D3.anode
  N53: Q3.C, Ry3.connector0, D4.anode
  Ry4: Q4.C, Ry4.connector0, D5.anode
  Ry5: Q5.C, Ry5.connector0, D6.anode
  N54: Q6.C, Ry6.connector0, D7.anode

notes:
  TCA - Turnout Control with Arduino, 6x Servo Switch Driver based on Arduino Micro R3 connecting to GCA/GC2, with Acknowledge, V1.0 r6
  DCC Track (DT) Power Bus
  J1 : Track 'TA' & 'TB'
  J2 : Frog Polarization S1..S6
  Relay HFD2
  ________
  Q1..Q6: BC 337-40
  Polymer
  5V= regulated
  1: +V ; 2: GND
  GC2: J3-7..10 = D13..D16
  Vcc - Fused
  on socket
  "Short Circuit"
  "Servo Ready"
  Connector J4: to GC2 J4
  Connectors S1..S6: to Servo/Switch S1..S6
  on GC2: J4-3..10 = D1..D8
  Connector J3: to GC2 J3
  Switch Pos Input 1..6 :
  Switch Pos ACK 1..6
  onGC2: D9..D12 : not used, free for other use
  '0'=straight ; '1'=round (static)
  D13..D16 = A2..A5 = S3..S6
  on GC2 J3-7..10 used (4-bit)
  J4-9..10: D7..D8 = A0..A1 = S1..S2
  Switch Position S1..S6
  "Power ON"
  LED S1..S6 : ON = round
  Ry1..Ry6: HFD2
  D1..D7: 1N4001
  Power Up Completed
  ACK 1..6 = changes (static) after
  Servo/Switch Pos is reached
  Servo Lever Control
  Position, Travel, Direction, Speed:
  Controlled by Arduino SW, see Sketch
  Fuse
  '0' = straight, '1' = round
  1K
  10K
  -
  +
  TCA V1.0 r6
  Carlo Ritter
  140211
  2x 100nF
  68uF
  Vin
  "Short"
  HFD2
  1N4001
  Arduino
  Micro R3
  BC 337
  "Round"
  DCC
  Frog
  6 Out
  Servo
  Relay
  +5V
  reg
  1N4148
  6 In
  P
  Pin 1
  !! 1k too high !!
  INPUT Switch Pos 1..6 : A0-A5
  OUTPUT Switch ACK 1..6 :
  !! Verpolungsschutzdiode !!
  1. S6-7 shorts: cut track on upper side of PCB, both sides of pin
  then connect S6-10 to J2-5 on bottom side of PCB
  2. Servo connectors: + and pulse pins are interchanged for servo connector
  4. Polymer fuse: has too high on resistance, replace with std. fuse
  WARNING ! - current ERRORS: update to follow
  3. Relays: + and - of coil connections are interchanged
  or put before 5V regulator
