# Fritzing sketch id4018_TCA_140827_v2.1_r3_gold_0 (saved by Fritzing 0.9.0b)
circuit board: 9.6cm x 6.1cm
breadboards: 1

parts:
  S6 = male pin header, 3 pins [form="♂ (male)"]
  S5 = male pin header, 3 pins [form="♂ (male)"]
  S4 = male pin header, 3 pins [form="♂ (male)"]
  S3 = male pin header, 3 pins [form="♂ (male)"]
  S2 = male pin header, 3 pins [form="♂ (male)"]
  S1 = male pin header, 3 pins [form="♂ (male)"]
  D13 = Rectifier Diode [part_number=1N4001 package="300 mil [THT]"]
  R41 = Resistor [tolerance=±5% resistance=4.7k package=THT]
  R42 = Resistor [tolerance=±5% resistance=4.7k package=THT]
  R43 = Resistor [tolerance=±5% resistance=4.7k package=THT]
  R44 = Resistor [tolerance=±5% resistance=4.7k package=THT]
  R45 = Resistor [tolerance=±5% resistance=4.7k package=THT]
  R46 = Resistor [tolerance=±5% resistance=4.7k package=THT]
  R47 = Resistor [tolerance=±5% resistance=470 package=THT]
  R48 = Resistor [tolerance=±5% resistance=470 package=THT]
  R49 = Resistor [tolerance=±5% resistance=470 package=THT]
  R50 = Resistor [tolerance=±5% resistance=470 package=THT]
  R51 = Resistor [tolerance=±5% resistance=470 package=THT]
  R52 = Resistor [tolerance=±5% resistance=470 package=THT]
  R53 = Resistor [tolerance=±5% resistance=470 package=THT]
  R54 = Resistor [tolerance=±5% resistance=470 package=THT]
  R55 = Resistor [tolerance=±5% resistance=470 package=THT]
  R56 = Resistor [tolerance=±5% resistance=470 package=THT]
  R57 = Resistor [tolerance=±5% resistance=470 package=THT]
  R58 = Resistor [tolerance=±5% resistance=470 package=THT]
  R59 = Resistor [tolerance=±5% resistance=470 package=THT]
  R60 = Resistor [tolerance=±5% resistance=470 package=THT]
  R61 = Resistor [tolerance=±5% resistance=470 package=THT]
  R62 = Resistor [tolerance=±5% resistance=470 package=THT]
  R64 = Resistor [tolerance=±5% resistance=470 package=THT]
  Fu = prefix0000
  C5 = Ceramic Capacitor [capacitance=100nF voltage=35V package="200 mil [THT, multilayer]"]
  C6 = Ceramic Capacitor [capacitance=100nF voltage=35V package="200 mil [THT, multilayer]"]
  D14 = Rectifier Diode [part_number=1N4148 package="300 mil [THT]"]
  J4 = male pin header, 10 pins [form="♂ (male)"]
  J3 = male pin header, 4 pins [form="♂ (male)"]
  J2 = male pin header, 6 pins [form="♂ (male)"]
  Q7 = NPN-Transistor [package="TO92 [THT]"]
  Q8 = NPN-Transistor [package="TO92 [THT]"]
  Q9 = NPN-Transistor [package="TO92 [THT]"]
  Q10 = NPN-Transistor [package="TO92 [THT]"]
  Q11 = NPN-Transistor [package="TO92 [THT]"]
  Q12 = NPN-Transistor [package="TO92 [THT]"]
  Arduino_Micro_R3 = Arduino Micro (Rev3)
  R34 = Resistor [tolerance=±5% resistance=1k package=THT]
  LED4 = LED - 3mm [color="Red (633nm)" package="3 mm [THT]"]
  J10 = male pin header, 3 pins [form="♂ (male)"]
  J11 = male pin header, 1 pin [form="♂ (male)"]
  J12 = male pin header, 1 pin [form="♂ (male)"]
  D15 = Rectifier Diode [part_number=1N4001 package="300 mil [THT]"]
  J13 = male pin header, 3 pins [form="♂ (male)"]
  J14 = male pin header, 1 pin [form="♂ (male)"]
  J15 = male pin header, 1 pin [form="♂ (male)"]
  D16 = Rectifier Diode [part_number=1N4001 package="300 mil [THT]"]
  J16 = male pin header, 3 pins [form="♂ (male)"]
  J17 = male pin header, 1 pin [form="♂ (male)"]
  J18 = male pin header, 1 pin [form="♂ (male)"]
  D17 = Rectifier Diode [part_number=1N4001 package="300 mil [THT]"]
  J19 = male pin header, 3 pins [form="♂ (male)"]
  J20 = male pin header, 1 pin [form="♂ (male)"]
  J21 = male pin header, 1 pin [form="♂ (male)"]
  D18 = Rectifier Diode [part_number=1N4001 package="300 mil [THT]"]
  J22 = male pin header, 3 pins [form="♂ (male)"]
  J23 = male pin header, 1 pin [form="♂ (male)"]
  J24 = male pin header, 1 pin [form="♂ (male)"]
  D19 = Rectifier Diode [part_number=1N4001 package="300 mil [THT]"]
  J25 = male pin header, 3 pins [form="♂ (male)"]
  J26 = male pin header, 1 pin [form="♂ (male)"]
  J27 = male pin header, 1 pin [form="♂ (male)"]
  D20 = Rectifier Diode [part_number=1N4001 package="300 mil [THT]"]
  R63 = Resistor [tolerance=±5% resistance=470 package=THT]
  C4 = Tantalum Capacitor [capacitance=47µF voltage=16V package="100 mil [THT, tantalum]"]
  J1 = male pin header, 2 pins [form="♂ (male)"]
  7805 = Voltage Regulator - 5V [package="TO220 [THT]"]
  C7 = Tantalum Capacitor [capacitance=47µF voltage=16V package="100 mil [THT, tantalum]"]
  D21 = Rectifier Diode [part_number=1N4001 package="300 mil [THT]"]
  C8 = Ceramic Capacitor [capacitance=100nF voltage=35V package="200 mil [THT, multilayer]"]
  AKL = Screw terminal - 2 pins [package=THT]
  J28 = male pin header, 1 pin [form="♂ (male)"]  # not connected
  GOLD1 = male pin header, 3 pins [form="♂ (male)"]  # not connected
  GOLD2 = male pin header, 2 pins [form="♂ (male)"]  # not connected
  GOLD = male pin header, 4 pins [form="♂ (male)"]  # not connected

nets:
  S6: S6.pin1, R53.Pin_1
  5V: S6.pin2, S5.pin2, S4.pin2, S3.pin2, S2.pin2, S1.pin2, D13.cathode, C5.1, Arduino_Micro_R3.5V, J11.pin1, D15.cathode, J15.pin1, D16.cathode, J17.pin1, D17.cathode, J21.pin1, D18.cathode, J24.pin1, D19.cathode, J26.pin1, 7805.output_voltage, C7.+, D21.anode, C8.1
  GND: S6.pin3, S5.pin3, S4.pin3, S3.pin3, S2.pin3, S1.pin3, C5.0, C6.0, J4.pin2, Q7.E, Q8.E, Q9.E, Q10.E, Q11.E, Q12.E, Arduino_Micro_R3.GND, C4.-, 7805.GND, C7.-, C8.0, AKL.pin2
  S5: S5.pin1, R54.Pin_1
  S4: S4.pin1, R55.Pin_1
  S3: S3.pin1, R56.Pin_1
  S2: S2.pin1, R57.Pin_1
  S1: S1.pin1, R58.Pin_1
  N1: D13.anode, Q12.C, J12.pin1
  N2: R41.Pin_0, R47.Pin_0, Arduino_Micro_R3.D6_PWM/A7
  N3: R41.Pin_1, Q7.B
  N4: R42.Pin_0, R48.Pin_0, Arduino_Micro_R3.D5_PWM
  N5: R42.Pin_1, Q8.B
  N6: R43.Pin_0, R49.Pin_0, Arduino_Micro_R3.D4_PWM/A6
  N7: R43.Pin_1, Q9.B
  N8: R44.Pin_0, R50.Pin_0, Arduino_Micro_R3.D3/SCL
  N9: R44.Pin_1, Q10.B
  N10: R45.Pin_0, R51.Pin_0, Arduino_Micro_R3.D2/SDA
  N11: R45.Pin_1, Q11.B
  N12: R46.Pin_0, R52.Pin_0, Arduino_Micro_R3.D1/TX
  N13: R46.Pin_1, Q12.B
  N14: R47.Pin_1, J4.pin8
  N15: R48.Pin_1, J4.pin7
  N16: R49.Pin_1, J4.pin6
  N17: R50.Pin_1, J4.pin5
  N18: R51.Pin_1, J4.pin4
  N19: R52.Pin_1, J4.pin3
  N20: R53.Pin_0, Arduino_Micro_R3.D12_PWM/A11
  N21: R54.Pin_0, Arduino_Micro_R3.D11_PWM
  N22: R55.Pin_0, Arduino_Micro_R3.D10_PWM/A10
  N23: R56.Pin_0, Arduino_Micro_R3.D9_PWM/A9
  N24: R57.Pin_0, Arduino_Micro_R3.D8_PWM/A8
  N25: R58.Pin_0, Arduino_Micro_R3.D7
  N26: R59.Pin_0, J3.pin4
  N27: R59.Pin_1, Arduino_Micro_R3.A5
  N28: R60.Pin_0, J3.pin3
  N29: R60.Pin_1, Arduino_Micro_R3.A4
  N30: R61.Pin_0, J3.pin2
  N31: R61.Pin_1, Arduino_Micro_R3.A3
  N32: R62.Pin_0, J3.pin1
  N33: R62.Pin_1, Arduino_Micro_R3.A2
  A0: R64.Pin_0, J4.pin9
  N34: R64.Pin_1, Arduino_Micro_R3.A0
  N35: Fu.connector0, R34.Pin_0, D20.cathode
  N36: Fu.connector1, C6.1, D14.cathode, C4.+, 7805.input_voltage, D21.cathode
  N37: D14.anode, LED4.cathode
  A1: J4.pin10, R63.Pin_0
  N38: J2.pin1, J10.pin1
  N39: J2.pin2, J13.pin1
  N40: J2.pin3, J16.pin1
  N41: J2.pin4, J19.pin1
  N42: J2.pin5, J22.pin1
  N43: J2.pin6, J25.pin1
  N44: Q7.C, D19.anode, J27.pin1
  N45: Q8.C, D18.anode, J23.pin1
  N46: Q9.C, D17.anode, J20.pin1
  N47: Q10.C, D16.anode, J18.pin1
  N48: Q11.C, D15.anode, J14.pin1
  N49: Arduino_Micro_R3.A1, R63.Pin_1
  N50: R34.Pin_1, LED4.anode
  TA: J10.pin2, J13.pin2, J16.pin2, J19.pin2, J22.pin2, J25.pin2, J1.pin1
  TB: J10.pin3, J13.pin3, J16.pin3, J19.pin3, J22.pin3, J25.pin3, J1.pin2
  N51: D20.anode, AKL.pin1

notes:
  TCA - Turnout Control with Arduino, 6x Servo Switch Driver based on Arduino Micro R3 connecting to GCA/GC2 or other, with Ack, V2.1 r3
  '0' = straight, '1' = round
  Arduino SW, see Sketch
  Position, Travel, Direction, Speed:
  Servo Lever Control:
  Servo/Switch Pos is reached
  ACK 1..6 = changes (static) after
  Power Up Completed
  D: 1N4001
  Relay: HFD2
  J4-9..10: D7..D8 = A0..A1 = S1..S2
  on GC2 J3-7..10 used (4-bit)
  D13..D16 = A2..A5 = S3..S6
  '0'=straight ; '1'=round (static)
  on GC2: D9..D12 : not used
  Switch Pos ACK 1..6
  OUTPUT Switch ACK 1..6 :
  INPUT Switch Pos 1..6 : A0-A5
  Switch Pos Input 1..6 :
  Connector J3: to GC2 J3
  on GC2: J4-3..10 = D1..D8
  Connectors S1..S6: to Servo/Switch S1..S6
  Connector J4: to GC2 J4
  LED D13: "Servo Ready"
  "Short Circuit"
  on socket
  Vcc
  GC2: J3-7..10 = D13..D16
  1: +10 to 12 V
  Polymer Fuse
  Q: BC 337-40
  Relay 1
  J2 : Frog S1..S6
  J1 : Track Bus
  DCC Track (DT) Power Bus
  cl
  +
  C
  A
  R
  A rbeit / A ctive
  R uhe / R est
  C ommon
  (Arduino: D1..D6)
  cl : coil
  Relay 2
  Relay 3
  Relay 4
  Relay 5
  m
  Relay 6
  2: GND
  Polarization
  J3-3..6 free for other use
  OUTPUT Servo S1..S6
  D7..D12
  Ry1
  Ry2
  Ry3
  Ry4
  Ry5
  Ry6
  1N4001
  BC337
  1N4148
  100nF
  47uF
  4k7
  470
  PSS 254/2G
  PSS 254/3G
  PSS 254/4G
  PSS 254/6G
  PSS 254/10G
  HFD2/5V
  TCA - V2.1 r3
  Carlo Ritter
  140308
  1K
  SHORT
  LED
  GND
  1
  +12V
  34
  Pulse
  -
  DCC
  Frog
  DT
  LP60-050
  AKL 220-02
