# Fritzing sketch id401_arduino_isp_0 (saved by Fritzing 0.9.3b)
breadboards: 1

parts:
  Part1 = Arduino Nano (Rev3.0) (ICSP)
  Part2 = Arduino Nano (Rev3.0) (ICSP)
  C1 = Electrolytic Capacitor [capacitance=10µF package="100 mil [THT, electrolytic]"]

nets:
  N1: Part1.RESET, Part2.D10
  GND: Part1.GND, Part2.GND, C1.-
  N2: Part1.D11/MOSI, Part2.D11/MOSI
  N3: Part1.D12/MISO, Part2.D12/MISO
  5V: Part1.5V, Part2.5V
  N4: Part1.D13/SCK, Part2.D13/SCK
  N5: Part2.RESET, C1.+
