# Fritzing sketch id4020_Untitled_Sketch_0 (saved by Fritzing 0.7.12b)
breadboards: 2

parts:
  Arduino = Arduino
  LCD = LCD screen
  DHT11_-_Sensor_de_Umidade_e_Temperatura = DHT11_Temperature_and_Humitidy_Sensor
  R2 = 1.5k Ω Resistor [package=THT]
  Sensor_de_Luminosidade = Photocell (LDR) [package=THT]
  R4 = 10k Ω Resistor [package=THT]
  Motor_Janela = DC Motor

nets:
  N1: Arduino.D13, Motor_Janela.pin_1
  N2: Arduino.D12, Motor_Janela.pin_2
  N3: Arduino.D5, LCD.DB7
  N4: Arduino.D4, LCD.DB6
  N5: Arduino.D3, LCD.DB5
  N6: Arduino.D1TX, LCD.E
  N7: Arduino.D0RX, LCD.RS
  +5V: Arduino.+5V, LCD.VDD, DHT11_-_Sensor_de_Umidade_e_Temperatura.connector1
  GND: Arduino.GND, LCD.VSS, LCD.R/W, LCD.LED-, DHT11_-_Sensor_de_Umidade_e_Temperatura.connector4, R2.Pin_1, Sensor_de_Luminosidade.pin_1, R4.Pin_0
  N8: Arduino.A0, DHT11_-_Sensor_de_Umidade_e_Temperatura.connector2
  N9: Arduino.A1, Sensor_de_Luminosidade.pin_0, R4.Pin_1
  N10: LCD.V0, R2.Pin_0
