# Fritzing sketch id4021_OpenStim_0 (saved by Fritzing 0.8.7b)
circuit board: 5.89814cm x 5.28415cm
breadboards: 1

parts:
  Ch_1 = BANANA_CONN [package=banana_conn]
  R1 = Resistor [tolerance=±5% resistance=17 package=THT]
  Ref = BANANA_CONN [package=banana_conn]
  Arduino_Nano = Arduino Nano (Rev3.0)
  Ch_5 = BANANA_CONN [package=banana_conn]
  Ch_3 = BANANA_CONN [package=banana_conn]
  Ch_4 = BANANA_CONN [package=banana_conn]
  Active_LED = LED - 5mm [color="Red (633nm)" package="5 mm [THT]"]
  Ch_2 = BANANA_CONN [package=banana_conn]
  SPI_Pot = AD5206 Digital Potentiometer [maximum_resistance=10kΩ package="DIP28 [THT]"]

nets:
  N1: Ch_1.1, Arduino_Nano.D4
  N2: R1.Pin_0, Arduino_Nano.A6, SPI_Pot.A6
  N3: R1.Pin_1, Arduino_Nano.D2
  N4: Ref.1, SPI_Pot.W6
  GND: Arduino_Nano.GND, Active_LED.cathode, SPI_Pot.Gnd, SPI_Pot.Vss
  N5: Arduino_Nano.D3, Active_LED.anode
  N6: Arduino_Nano.D5, Ch_2.1
  N7: Arduino_Nano.D6, Ch_3.1
  N8: Arduino_Nano.D7, Ch_4.1
  N9: Arduino_Nano.D8, Ch_5.1
  N10: Arduino_Nano.D10, SPI_Pot.CS
  N11: Arduino_Nano.D11/MOSI, SPI_Pot.SDI
  5V: Arduino_Nano.5V, SPI_Pot.Vdd

notes:
  Open Stim
  https://sourceforge.net/projects/openbrainstim/
  Schematic Ref: http://sourceforge.net/p/openbrainstim/wiki/Hardware/attachment/openstim-multichannel_schem.jpg
  Please check for accuracy and errors before building.
  This document shall inherit the license of the project. GPLv3
  Version 1: Power source not include, Breadboard is oversized, routing and layout are NOT optimized
