# Fritzing sketch id4022_Intro_to_ENG_spinny_motor_NEW_Electronics_project_0 (saved by Fritzing 0.9.3b)
breadboards: 1

parts:
  Part1 = Arduino Uno (Rev3) - ICSP
  R2 = Rotary Potentiometer (Small) [maximum_resistance=100kΩ package=THT]
  S1 = Pushbutton [package="[SMD]"]
  S2 = Pushbutton [package="[SMD]"]
  M1 = DC Motor
  VCC1 = Battery block 9V
  IC1 = H-Bridge [package=THT]
  U1 = Voltage Regulator - Variable [package="TO220 [THT]"]

nets:
  N1: Part1.A0, R2.wiper
  N2: Part1.D9_PWM, U1.ADJ
  GND: Part1.D2, Part1.GND, R2.leg1, S2.Pin_1, S2.Pin_2, VCC1.-, IC1.GND3, IC1.GND4, U1.IN
  N3: Part1.D4, Part1.5V, R2.leg2, S1.Pin_3, S1.Pin_4, VCC1.+, IC1.VCC2, IC1.3_4EN, IC1.VCC1
  N4: Part1.D5_PWM, IC1.4A
  N5: Part1.D6_PWM, IC1.3A
  N6: S1.Pin_1, S1.Pin_2, M1.pin_1, IC1.3Y, U1.OUT
  N7: S2.Pin_3, S2.Pin_4, M1.pin_2, IC1.4Y
