# Fritzing sketch id4024_Fritzing_Jack_0 (saved by Fritzing 0.9.2b)
breadboards: 1

parts:
  R1 = Rotary Potentiometer (Small) [maximum_resistance=100kΩ package=THT]
  Part1 = Arduino Uno (Rev3)
  VCC1 = Battery
  U1 = 2.4GHz Low Power Transceiver [package=qfn20]

nets:
  N1: R1.leg1, Part1.GND, VCC1.-, U1.CE
  N2: R1.wiper, Part1.A0
  N3: R1.leg2, Part1.5V, VCC1.+
  N4: Part1.D9_PWM, U1.SCK
  N5: Part1.D10_PWM/SS, U1.MOSI
  N6: Part1.D11_PWM/MOSI, U1.IRQ
  N7: Part1.D12/MISO, U1.VDD
  N8: Part1.D13/SCK, U1.MISO
  N9: Part1.3V3, U1.CSN
