# Fritzing sketch id4025_techlab_0 (saved by Fritzing 0.9.3b)
breadboards: 1

parts:
  Raspberry_Pi_1 = Raspberry Pi 3 [part_number=RPI-3-V1.2]
  RHT1 = Humidity and Temperature Sensor RHT03
  S1 = Round Pushbutton
  Grove1 = Grove OLED 128x96

nets:
  3V3: Raspberry_Pi_1.3v3, Grove1.VCC
  N1: Raspberry_Pi_1.GPIO2, Grove1.SDA
  N2: Raspberry_Pi_1.GPIO3, Grove1.SCL
  N3: Raspberry_Pi_1.GPIO4, RHT1.Data-signal
  N4: Raspberry_Pi_1.GPIO10, RHT1.Vcc
  GND: Raspberry_Pi_1.GND, RHT1.GND_2, S1.leg1, Grove1.GND
  N5: Raspberry_Pi_1.GPIO21, S1.leg0

notes:
  + / out / -
