# Fritzing sketch id4026_bateau_0 (saved by Fritzing 0.9.3b)
breadboards: 1

parts:
  Composant1 = Arduino Uno (Rev3)
  Moteur_VOILE = DC Motor
  Moteur_DEPLACEMENT = DC Motor
  Moteur_AILERON = DC Motor
  IC1 = H-Bridge [package=THT]
  IC2 = H-Bridge [package=THT]
  R1 = Resistor [tolerance=±5% resistance=1k package=THT]
  R2 = Resistor [tolerance=±5% resistance=1k package=THT]
  U1 = SWITCH_SPDT [package=kps-1290]
  Composant2 = Bluetooth HC-05 Macho
  VCC1 = Battery block 9V
  VCC2 = Battery block 9V  # not connected

nets:
  N1: Composant1.A0, R1.Pin_1, U1.S
  N2: Composant1.A1, R2.Pin_1, U1.O
  N3: Composant1.D8, IC1.4A
  N4: Composant1.D9_PWM, IC2.3_4EN
  N5: Composant1.D10_PWM/SS, IC2.3A
  N6: Composant1.D11_PWM/MOSI, IC2.4A
  N7: Composant1.D0/RX, Composant2.TXD
  N8: Composant1.D1/TX, Composant2.RXD
  N9: Composant1.D3_PWM, IC1.1_2EN
  N10: Composant1.D4, IC1.1A
  N11: Composant1.D5_PWM, IC1.2A
  N12: Composant1.D6_PWM, IC1.3_4EN
  N13: Composant1.D7, IC1.3A
  5V: Composant1.5V, IC1.VCC1, IC2.VCC1, U1.P, Composant2.VCC
  GND: Composant1.GND, IC1.GND1, IC1.GND2, IC1.GND3, IC1.GND4, IC2.GND1, IC2.GND2, IC2.GND3, IC2.GND4, R1.Pin_0, R2.Pin_0, Composant2.GND, VCC1.-
  N14: Moteur_VOILE.pin_1, IC1.4Y
  N15: Moteur_VOILE.pin_2, IC1.3Y
  N16: Moteur_DEPLACEMENT.pin_1, IC2.4Y
  N17: Moteur_DEPLACEMENT.pin_2, IC2.3Y
  N18: Moteur_AILERON.pin_1, IC1.2Y
  N19: Moteur_AILERON.pin_2, IC1.1Y
  N20: IC1.VCC2, IC2.VCC2, VCC1.+
