# Fritzing sketch id4027_TeenAstroV2_0 (saved by Fritzing 0.9.3b)
circuit board: 10cm x 8cm
breadboards: 2

parts:
  TMC2100 = Pololu A4988 [package=SO16]
  Power_plug_12V = Power plug
  Teensy_3_1_for_Focuser = Teensy 3.1
  Teensy_3_1_for_Telescope = Teensy 3.1
  C2 = Capacitor Polarized [package=cpol-radial-100uf-25v]
  C3 = Capacitor Polarized [package=cpol-radial-100uf-25v]
  1B_1A_2A_2B = screw terminal, 4 pins
  R2 = Resistor [tolerance=±5% resistance=10k package="1206 [SMD]"]
  R1 = Resistor [tolerance=±5% resistance=10k package="1206 [SMD]"]
  R3 = Resistor [tolerance=±5% resistance=10k package="1206 [SMD]"]
  R4 = Resistor [tolerance=±5% resistance=10k package="1206 [SMD]"]
  R5 = Resistor [tolerance=±5% resistance=10k package="1206 [SMD]"]
  R6 = Resistor [tolerance=±5% resistance=10k package="1206 [SMD]"]
  R7 = Resistor [tolerance=±5% resistance=10k package="1206 [SMD]"]
  R8 = Resistor [tolerance=±5% resistance=10k package="1206 [SMD]"]
  HdCrtlr = female pin header, 7 pins [form="♀ (female)"]
  DS1302 = DS1302 [package="DIP8 [THT]"]
  USB_CONN2 = USB connector [package=THT]
  USB_CONN1 = USB connector [package=THT]
  USB1 = female pin header, 2 pins [form="♀ (female)"]
  USB2 = female pin header, 2 pins [form="♀ (female)"]
  Fuse = FUSE [package=fuse_5mm]
  RA = female pin header, 3 pins [form="♀ (female)"]
  DEC = female pin header, 3 pins [form="♀ (female)"]
  Optional_Digital_Pins = female pin header, 7 pins [form="♀ (female)"]
  VMot = Screw terminal - 2 pins [package=THT]
  3_3V_Gnd = female pin header, 2 pins [form="♀ (female)"]
  BAT2 = Battery Holders [package=battcon_12mm_pth]
  HdFoc = female pin header, 2 pins [form="♀ (female)"]
  12V_to_3_3V = Voltage Regulator - 3.3V [package="TO220 [THT]"]
  Optional_Analog_Pins = female pin header, 12 pins [form="♀ (female)"]
  C1 = Capacitor Polarized [package=cpol-radial-100uf-25v]
  X1_X2 = female pin header, 2 pins [form="♀ (female)"]
  D3 = Rectifier Diode 10A [part_number=P1000K]

nets:
  GND: TMC2100.ENABLE, TMC2100.GND, Power_plug_12V.GND, Teensy_3_1_for_Focuser.GND, Teensy_3_1_for_Telescope.GND, C2.-, C3.-, R2.Pin_1, R1.Pin_1, DS1302.0V, USB_CONN2.GND, USB_CONN2.chassis5, USB_CONN2.chassis6, USB_CONN1.GND, USB_CONN1.chassis5, USB_CONN1.chassis6, Optional_Digital_Pins.pin1, VMot.pin1, 3_3V_Gnd.pin2, BAT2.-, 12V_to_3_3V.GND, C1.-, D3.anode
  N1: TMC2100.STEP, Teensy_3_1_for_Focuser.D5
  N2: TMC2100.DIR, Teensy_3_1_for_Focuser.D6
  3V3: TMC2100.VDD, Teensy_3_1_for_Focuser.3V3, Teensy_3_1_for_Telescope.3V3, C2.+, HdCrtlr.pin7, DS1302.+V, Optional_Digital_Pins.pin7, 3_3V_Gnd.pin1, 12V_to_3_3V.output_voltage, Optional_Analog_Pins.pin2
  N3: TMC2100.1B, 1B_1A_2A_2B.pin1
  N4: TMC2100.1A, 1B_1A_2A_2B.pin2
  N5: TMC2100.2A, 1B_1A_2A_2B.pin3
  N6: TMC2100.2B, 1B_1A_2A_2B.pin4
  N7: TMC2100.VMOT, C3.+, Fuse.2, VMot.pin2, 12V_to_3_3V.input_voltage, C1.+, D3.cathode
  N8: Power_plug_12V.VCC, Fuse.1
  N9: Teensy_3_1_for_Focuser.D2, DS1302.SCLK_-_SPI_Clock
  N10: Teensy_3_1_for_Focuser.D3, DS1302.I/O_-_SPI_Data_In/Out
  N11: Teensy_3_1_for_Focuser.D4, DS1302.CE_-_Chip_Enable
  N12: Teensy_3_1_for_Focuser.D7, R1.Pin_0, HdFoc.pin2
  N13: Teensy_3_1_for_Focuser.D8, R2.Pin_0, HdFoc.pin1
  N14: Teensy_3_1_for_Focuser.A0/D14, Optional_Analog_Pins.pin12
  N15: Teensy_3_1_for_Focuser.A1/D15, Optional_Analog_Pins.pin11
  N16: Teensy_3_1_for_Focuser.A2/D16, Optional_Analog_Pins.pin10
  N17: Teensy_3_1_for_Focuser.A3/D17, Optional_Analog_Pins.pin9
  N18: Teensy_3_1_for_Focuser.A4/D18, Optional_Analog_Pins.pin8
  N19: Teensy_3_1_for_Focuser.A5/D19, Optional_Analog_Pins.pin7
  N20: Teensy_3_1_for_Focuser.A6/D20, Optional_Analog_Pins.pin6
  N21: Teensy_3_1_for_Focuser.A7/D21, Optional_Analog_Pins.pin5
  N22: Teensy_3_1_for_Focuser.A8/D22, Optional_Analog_Pins.pin4
  N23: Teensy_3_1_for_Focuser.A9/D23, Optional_Analog_Pins.pin3
  N24: Teensy_3_1_for_Focuser.AGND, Optional_Analog_Pins.pin1
  N25: Teensy_3_1_for_Telescope.D2, RA.pin3
  N26: Teensy_3_1_for_Telescope.D3, RA.pin2
  N27: Teensy_3_1_for_Telescope.D4, RA.pin1
  N28: Teensy_3_1_for_Telescope.D5, Optional_Digital_Pins.pin6
  N29: Teensy_3_1_for_Telescope.D6, Optional_Digital_Pins.pin5
  N30: Teensy_3_1_for_Telescope.D7, Optional_Digital_Pins.pin4
  N31: Teensy_3_1_for_Telescope.D8, Optional_Digital_Pins.pin3
  N32: Teensy_3_1_for_Telescope.D9, Optional_Digital_Pins.pin2
  N33: Teensy_3_1_for_Telescope.D10, DEC.pin3
  N34: Teensy_3_1_for_Telescope.D11, DEC.pin2
  N35: Teensy_3_1_for_Telescope.D12, DEC.pin1
  N36: Teensy_3_1_for_Telescope.VBat, DS1302.Vbat_-_Backup_Supply, BAT2.+
  N37: Teensy_3_1_for_Telescope.A1/D15, R8.Pin_0, HdCrtlr.pin1
  N38: Teensy_3_1_for_Telescope.A2/D16, R7.Pin_0, HdCrtlr.pin2
  N39: Teensy_3_1_for_Telescope.A3/D17, R6.Pin_0, HdCrtlr.pin3
  N40: Teensy_3_1_for_Telescope.A4/D18, R5.Pin_0, HdCrtlr.pin4
  N41: Teensy_3_1_for_Telescope.A5/D19, R4.Pin_0, HdCrtlr.pin5
  N42: Teensy_3_1_for_Telescope.A6/D20, R3.Pin_0, HdCrtlr.pin6
  N43: Teensy_3_1_for_Telescope.AGND, R3.Pin_1, R4.Pin_1, R5.Pin_1, R6.Pin_1, R7.Pin_1, R8.Pin_1
  N44: DS1302.X1_-_Crystal, X1_X2.pin2
  N45: DS1302.X2_-_Crystal, X1_X2.pin1
  N46: USB_CONN2.d-, USB2.pin2
  N47: USB_CONN2.d+, USB2.pin1
  N48: USB_CONN1.d-, USB1.pin2
  N49: USB_CONN1.d+, USB1.pin1
