# Fritzing sketch id4028_FS_15_Button_Box_0 (saved by Fritzing 0.9.2b)
breadboards: 1

parts:
  Teensy_3_1 = Teensy 3.1
  S1 = SWITCH-MOMENTARY-2 [package=tactile_switch_smd-2]
  S2 = SWITCH-MOMENTARY-2 [package=tactile_switch_smd-2]
  S3 = SWITCH-MOMENTARY-2 [package=tactile_switch_smd-2]
  S4 = SWITCH-MOMENTARY-2 [package=tactile_switch_smd-2]
  S5 = SWITCH-MOMENTARY-2 [package=tactile_switch_smd-2]
  S6 = SWITCH-MOMENTARY-2 [package=tactile_switch_smd-2]
  S7 = SWITCH-MOMENTARY-2 [package=tactile_switch_smd-2]
  S8 = SWITCH-MOMENTARY-2 [package=tactile_switch_smd-2]
  S9 = SWITCH-MOMENTARY-2 [package=tactile_switch_smd-2]
  S10 = SWITCH-MOMENTARY-2 [package=tactile_switch_smd-2]
  S11 = SWITCH-MOMENTARY-2 [package=tactile_switch_smd-2]
  S12 = SWITCH-MOMENTARY-2 [package=tactile_switch_smd-2]
  S13 = SWITCH-MOMENTARY-2 [package=tactile_switch_smd-2]
  S14 = SWITCH-MOMENTARY-2 [package=tactile_switch_smd-2]
  S15 = SWITCH-MOMENTARY-2 [package=tactile_switch_smd-2]
  S16 = SWITCH-MOMENTARY-2 [package=tactile_switch_smd-2]
  S19 = SWITCH-MOMENTARY-2 [package=tactile_switch_smd-2]
  S20 = SWITCH-MOMENTARY-2 [package=tactile_switch_smd-2]
  S21 = SWITCH-MOMENTARY-2 [package=tactile_switch_smd-2]
  S23 = SWITCH-MOMENTARY-2 [package=tactile_switch_smd-2]
  S24 = SWITCH-MOMENTARY-2 [package=tactile_switch_smd-2]
  S25 = SWITCH-MOMENTARY-2 [package=tactile_switch_smd-2]
  S26 = SWITCH-MOMENTARY-2 [package=tactile_switch_smd-2]
  S27 = SWITCH-MOMENTARY-2 [package=tactile_switch_smd-2]
  S28 = SWITCH-MOMENTARY-2 [package=tactile_switch_smd-2]
  S29 = SWITCH-MOMENTARY-2 [package=tactile_switch_smd-2]
  S30 = SWITCH-MOMENTARY-2 [package=tactile_switch_smd-2]
  S31 = SWITCH-MOMENTARY-2 [package=tactile_switch_smd-2]
  U1 = SWITCH_SPDT [package=kps-1290]

nets:
  N1: Teensy_3_1.GND, S1.2, S2.2, S3.2, S4.2, S5.2, S6.2, S7.2, S8.2, S9.2, S10.2, S11.2, S12.2, S24.2, S25.2, S26.2, S27.2, S28.2, S29.2, S30.2, S31.2
  N2: Teensy_3_1.D0, S14.1
  N3: Teensy_3_1.D1, S13.1
  N4: Teensy_3_1.D2, U1.O
  N5: Teensy_3_1.D3, U1.S
  N6: Teensy_3_1.D4, S19.1
  N7: Teensy_3_1.D5, S15.1
  N8: Teensy_3_1.D6, S16.1
  N9: Teensy_3_1.D7, S21.1
  N10: Teensy_3_1.D8, S20.1
  N11: Teensy_3_1.D9, S23.1
  N12: Teensy_3_1.A0/D14, S1.1
  N13: Teensy_3_1.A1/D15, S6.1
  N14: Teensy_3_1.A2/D16, S10.1
  N15: Teensy_3_1.A3/D17, S25.1
  N16: Teensy_3_1.A4/D18, S29.1
  N17: Teensy_3_1.A5/D19, S2.1
  N18: Teensy_3_1.A6/D20, S5.1
  N19: Teensy_3_1.A7/D21, S9.1
  N20: Teensy_3_1.A8/D22, S24.1
  N21: Teensy_3_1.A9/D23, S28.1
  N22: Teensy_3_1.3V3, S3.1
  N23: Teensy_3_1.AGND, S7.1
  N24: S13.2, S14.2, S15.2, S16.2, S19.2, S20.2, S21.2, S23.2, U1.P
