# Fritzing sketch id4029_DIPSY_CONFIG_0 (saved by Fritzing 0.9.2b)
circuit board: 8.46667cm x 5.64444cm
breadboards: 1

parts:
  IC1 = IC, DIP package, 8 pins [chip_label=DIPSY]
  Teensy_3_1 = Teensy 3.1

nets:
  N1: IC1.pin1, Teensy_3_1.D0
  N2: IC1.pin2, Teensy_3_1.D2
  N3: IC1.pin3, Teensy_3_1.D1
  N4: IC1.pin4, Teensy_3_1.GND
  N5: IC1.pin5, Teensy_3_1.D11
  N6: IC1.pin7, Teensy_3_1.D13
  N7: IC1.pin8, Teensy_3_1.3V3

notes:
  System On Chip, a small Field Programmable Device that can be configured
  by TEENSY to implement different hardware functions. Minimal connections are displayed, DIPSY is configured and can be used as write only SPI Peripheral
  Hackaday Best Product Price Finalist 2015
  HTTP://DIPSY.COOL
  https://hackaday.io/project/6592-dipsy
