# Fritzing sketch id4030_Culm_0 (saved by Fritzing 0.9.2b)
breadboards: 2

parts:
  Part1 = Arduino Uno (Rev3)
  Part2 = FONA_SMA
  BATT1 = LiPoly_Battery__1300mAh
  R1 = Resistor [tolerance=±5% resistance=220 package=THT]
  S1 = Pushbutton [package="[THT]"]
  S2 = Pushbutton [package="[THT]"]
  S3 = Pushbutton [package="[THT]"]
  S4 = Pushbutton [package="[THT]"]
  S5 = Pushbutton [package="[THT]"]
  R2 = Resistor [tolerance=±5% resistance=220 package=THT]
  R3 = Resistor [tolerance=±5% resistance=220 package=THT]
  R4 = Resistor [tolerance=±5% resistance=220 package=THT]
  R5 = Resistor [tolerance=±5% resistance=220 package=THT]
  R6 = Rotary Potentiometer (Small) [maximum_resistance=100kΩ package=THT]
  Part3 = SRF05 Ultrasonic Rangefinder
  IC1 = L293D [package=THT]
  VCC1 = Battery block 9V
  J1 = Basic Servo

nets:
  N1: Part1.A0, R6.wiper
  N2: Part1.A2, S3.Pin_3, S3.Pin_4, R3.Pin_0
  N3: Part1.A4/SDA, S4.Pin_3, S4.Pin_4, R4.Pin_0
  N4: Part1.D8, Part3.connector10
  N5: Part1.D9_PWM, S5.Pin_4, R5.Pin_0
  N6: Part1.D10_PWM/SS, IC1.In_2
  N7: Part1.D11_PWM/MOSI, IC1.In_1
  N8: Part1.D12/MISO, S2.Pin_4, R2.Pin_0
  N9: Part1.D13/SCK, R1.Pin_0, S1.Pin_3, S1.Pin_4
  N10: Part1.D4, Part2.connector98
  N11: Part1.D5_PWM, Part2.connector99
  N12: Part1.D6_PWM, Part2.connector100
  N13: Part1.D7, Part3.connector9
  N14: Part1.5V, Part2.connector96, S1.Pin_1, S1.Pin_2, S2.Pin_1, S2.Pin_2, S3.Pin_1, S3.Pin_2, S4.Pin_1, S4.Pin_2, S5.Pin_1, S5.Pin_2, R6.leg1, Part3.connector8, IC1.Enable_1, IC1.+Vmotor, VCC1.+
  N15: Part1.GND, Part2.connector101, Part2.connector106, R1.Pin_1, R2.Pin_1, R3.Pin_1, R4.Pin_1, R5.Pin_1, R6.leg2, Part3.connector11, IC1.0V, VCC1.-
  N16: Part2.connector55, BATT1.connector2
  N17: Part2.connector56, BATT1.connector1
  N18: IC1.Out_1_(_Controlled_by_Enable_1_), J1.gnd
  N19: IC1.Out_2_(_Controlled_by_Enable_1_), J1.vcc

notes:
  Should be 500 mAh
  No fritzing model of Fingerprint Sensor available, this note is a placeholder
  The breadboard is split here
