# Fritzing sketch id4031_tank_0 (saved by Fritzing 0.9.3b)
circuit board: 6.88566cm x 5.36311cm
breadboards: 1

parts:
  M1 = DC Motor
  R1 = Resistor [tolerance=±5% resistance=10k package=THT]
  R2 = Resistor [tolerance=±5% resistance=10k package=THT]
  M2 = DC Motor
  SBDBT_R = FTDI_BASIC [package=ftdi_basic]
  SBDBT_L = FTDI_BASIC [package=ftdi_basic]
  3_3REG = Voltage Regulator - 3.3V [package="TO220 [THT]"]
  C1 = Ceramic Capacitor [capacitance=100nF package="100 mil [THT, multilayer]"]
  C2 = Capacitor Polarized [package=cpol-radial-10uf-25v]
  パーツ1 = Arduino Uno (Rev3)
  Vcc = Screw terminal - 2 pins [package=THT]
  TA7291P1 = ta7291p
  TA7291P2 = ta7291p

nets:
  N1: M1.pin_1, TA7291P1.connector2
  N2: M1.pin_2, TA7291P1.connector10
  N3: R1.Pin_0, TA7291P1.connector4
  N4: R1.Pin_1, R2.Pin_1, パーツ1.5V, Vcc.pin2, TA7291P1.connector7, TA7291P1.connector8, TA7291P2.connector7, TA7291P2.connector8
  N5: R2.Pin_0, TA7291P2.connector4
  N6: M2.pin_1, TA7291P2.connector2
  N7: M2.pin_2, TA7291P2.connector10
  N8: SBDBT_R.5, SBDBT_R.2
  N9: SBDBT_R.1, パーツ1.D12/MISO
  N10: SBDBT_R.3, パーツ1.D7
  N11: SBDBT_R.4, パーツ1.D6_PWM
  GND: SBDBT_L.3, 3_3REG.GND, C1.1, C2.-, パーツ1.GND, Vcc.pin1, TA7291P1.connector1, TA7291P2.connector1
  N12: SBDBT_L.4, 3_3REG.output_voltage, C2.+
  N13: 3_3REG.input_voltage, C1.0, パーツ1.VIN
  N14: パーツ1.D10_PWM/SS, TA7291P2.connector5
  N15: パーツ1.D11_PWM/MOSI, TA7291P2.connector6
  N16: パーツ1.D3_PWM, TA7291P1.connector5
  N17: パーツ1.D5_PWM, TA7291P1.connector6
