# Fritzing sketch id4032_Teleskop_0 (saved by Fritzing 0.9.3b)
breadboards: 1

parts:
  Bauteil1 = Arduino Mega ADK (Rev3)
  LCD1 = LCD screen
  R1 = Trimmer Potentiometer [maximum_resistance=10kΩ package=THT]
  M1 = Stepper Motor - Bipolar
  U1 = L298 [package=multiwatt15]
  Power_plug1 = Power plug
  U2 = L298 [package=multiwatt15]
  Bauteil2 = Thumb Joystick
  M2 = Stepper Motor - Bipolar

nets:
  N1: Bauteil1.A8, Bauteil2.VERT
  N2: Bauteil1.A9, Bauteil2.HORZ
  GND: Bauteil1.GND, LCD1.VSS, LCD1.R/W, LCD1.LED-, R1.leg1, U1.GND, Power_plug1.GND, U2.GND, Bauteil2.GND
  5V: Bauteil1.5V, LCD1.VDD, LCD1.LED+, R1.leg2, Bauteil2.VCC
  N3: Bauteil1.D2_PWM, LCD1.DB4
  N4: Bauteil1.D3_PWM, LCD1.DB5
  N5: Bauteil1.D4_PWM, LCD1.DB6
  N6: Bauteil1.D5_PWM, LCD1.DB7
  N7: Bauteil1.D6_PWM, LCD1.E
  N8: Bauteil1.D7_PWM, LCD1.RS
  N9: Bauteil1.D34, Bauteil2.SEL
  N10: Bauteil1.D36, U1.IN1
  N11: Bauteil1.D40, U1.IN2
  N12: Bauteil1.D42, U1.IN3
  N13: Bauteil1.D44, U1.IN4
  N14: Bauteil1.D46, U2.IN1
  N15: Bauteil1.D48, U2.ENA
  N16: Bauteil1.D50/MISO, U2.IN3
  N17: Bauteil1.D52/SCK, U2.IN4
  N18: LCD1.V0, R1.wiper
  N19: M1.A, U1.OUT1
  N20: M1.C, U1.OUT2
  N21: M1.B, U1.OUT3
  N22: M1.D, U1.OUT4
  N23: U1.VS, Power_plug1.VCC, U2.VS
  N24: U2.OUT1, M2.A
  N25: U2.OUT2, M2.C
  N26: U2.OUT3, M2.B
  N27: U2.OUT4, M2.D
