# Fritzing sketch id4033_teleduino_p_t_sketch_0 (saved by Fritzing 0.7.12b)
breadboards: 1

parts:
  Arduino_Uno_R3 = Arduino  # not connected
  5V_Relay = Relay [part_number="TTI TRB-5VDC-SB3-CD" package=THT]
  1N4001_Rectifier_Diode = Rectifier Diode [part_number=1N4001 package="300 mil [THT]"]
  1k_Ohm_Resistor_to_2N3904_Transistor_Base = Resistor [tolerance=±5% resistance=1k package=THT]
  2N3904_Transistor = NPN-Transistor [part_number=2N3904 package="TO92 [THT]"]
  TeleDuino_Status_Output_Blue_LED(5v) = LED - 5mm [color="Blue (430nm)" package="5 mm [THT]"]
  5V_Relay_LED(1_2v)_On/Off_Indicator = LED - 5mm [color="Red (633nm)" package="5 mm [THT]"]
  5V_DC_Input_Screw_Terminals = Screw terminal - 2 pins [package=THT]
  1k_ohm_resistor_to_Relay_LED_Anode = Resistor [tolerance=±5% resistance=1k package=THT]
  12V_DC_to_5V_Stepdown_Buck = Breadboard Power Supply Board SMD
  Arduino_Ethernet_Shield_stacked_onto_Uno_R3 = Arduino Ethernet Shield
  Align_DS410M_5V_Tilt_Servo = Basic Servo
  Align_DS410M_5V_Pan_Servo = Basic Servo

nets:
  N1: 5V_Relay.COIL1, 1N4001_Rectifier_Diode.anode, 2N3904_Transistor.C
  N2: 5V_Relay.C1, 5V_Relay.C2, 5V_Relay.COIL2, 1N4001_Rectifier_Diode.cathode, Arduino_Ethernet_Shield_stacked_onto_Uno_R3.+5V
  VCC: 5V_Relay.B, 1k_ohm_resistor_to_Relay_LED_Anode.Pin_0, Align_DS410M_5V_Tilt_Servo.vcc, Align_DS410M_5V_Pan_Servo.vcc
  N3: 1k_Ohm_Resistor_to_2N3904_Transistor_Base.Pin_0, Arduino_Ethernet_Shield_stacked_onto_Uno_R3.SS
  N4: 1k_Ohm_Resistor_to_2N3904_Transistor_Base.Pin_1, 2N3904_Transistor.B
  N5: 2N3904_Transistor.E, TeleDuino_Status_Output_Blue_LED(5v).cathode, 5V_Relay_LED(1_2v)_On/Off_Indicator.cathode, Arduino_Ethernet_Shield_stacked_onto_Uno_R3.GND#20
  N6: TeleDuino_Status_Output_Blue_LED(5v).anode, Arduino_Ethernet_Shield_stacked_onto_Uno_R3.D8
  N7: 5V_Relay_LED(1_2v)_On/Off_Indicator.anode, 1k_ohm_resistor_to_Relay_LED_Anode.Pin_1
  N8: 5V_DC_Input_Screw_Terminals.pin1, 12V_DC_to_5V_Stepdown_Buck.GND
  N9: 5V_DC_Input_Screw_Terminals.pin2, 12V_DC_to_5V_Stepdown_Buck.VCC
  GND: Arduino_Ethernet_Shield_stacked_onto_Uno_R3.GND#1, Align_DS410M_5V_Tilt_Servo.gnd, Align_DS410M_5V_Pan_Servo.gnd
  N10: Arduino_Ethernet_Shield_stacked_onto_Uno_R3.D9, Align_DS410M_5V_Pan_Servo.pulse
  N11: Arduino_Ethernet_Shield_stacked_onto_Uno_R3.D7, Align_DS410M_5V_Tilt_Servo.pulse
