# Fritzing sketch id4035_telegrafo2_0 (saved by Fritzing 0.9.2b)
breadboards: 1

parts:
  LED1 = LED - 5mm [color="Red (633nm)" package="5 mm [THT]"]
  LED2 = LED - 5mm [color="Blue (470nm)" package="5 mm [THT]"]
  J1 = COMPUTER-PERIPHERAL-POWER [package=computer-peripheral-power-ra]
  R1 = Resistor [tolerance=±10% resistance=380 package=THT]
  R2 = Resistor [tolerance=±5% resistance=380 package=THT]
  S1 = Pushbutton [package="[THT]"]

nets:
  N1: LED1.cathode, R2.Pin_0
  N2: LED2.anode, S1.Pin_1, S1.Pin_2
  N3: J1.5V, S1.Pin_3, S1.Pin_4
  N4: J1.GND, R1.Pin_0, R2.Pin_1

notes:
  CABLE DE ENTRADA DE DATOS
  ------------------------------------
  ESTE CABLE VIENE DESDE OTRO SET
  CABLE DE SALIDA DE DATOS
  -------------------------------
  ESTE CABLE VA HACIA OTRO SET
  FUENTE DE ENERGÍA
  Puede usarse una fuente de PC, aprovechando su salida de 5 V.
  Es conveniente que ambos equipos usen la misma fuente.
  Lista de Partes:
  - 2 x Resistor de 380 Ohm
  - 2 x LEDs de diferente color
  - 1 x Interruptor Botón
  - Protoboard
  - Cables para la conección
