# Fritzing sketch id4036_GP2_Orion_0 (saved by Fritzing 0.9.3b)
circuit board: 8.4cm x 6cm

parts:
  U1 = atmega328 [package=dip]
  XTAL1 = Crystal [frequency="16 Mhz" package=THT]
  C1 = Ceramic Capacitor [capacitance=22µF package="100 mil [THT, multilayer]"]
  C2 = Ceramic Capacitor [capacitance=22µF package="100 mil [THT, multilayer]"]
  D5_zero = Pushbutton [package="[THT]"]
  YES-_R1 = Resistor [tolerance=±5% resistance=220 package=THT]
  D4_Polaris = Pushbutton [package="[THT]"]
  A0_setAZI = Pushbutton [package="[THT]"]
  A4_setALT = Pushbutton [package="[THT]"]
  LCD = female pin header, 16 pins [form="♀ (female)"]
  TRIMPOT = Trimmer Potentiometer [maximum_resistance=10kΩ package=THT]
  encMan = female pin header, 3 pins [form="♀ (female)"]
  encMan_2 = female pin header, 2 pins [form="♀ (female)"]
  TRIMPOT1 = Trimmer Potentiometer [maximum_resistance=10kΩ package=THT]
  BAT+ = Pad [width=2.1630119375573931 height=3.8438016528925623 connect=center]
  GND = Pad [width=2.1630119375573931 height=3.8438016528925623 connect=center]
  GND_2 = Pad [width=2.1630119375573931 height=3.8438016528925623 connect=center]
  VCC = Pad [width=2.1630119375573931 height=3.8438016528925623 connect=center]
  encA1 = Pad [width=2.1630119375573931 height=3.8438016528925623 connect=center]
  encB1 = Pad [width=2.1630119375573931 height=3.8438016528925623 connect=center]
  encB2 = Pad [width=2.1630119375573931 height=3.8438016528925623 connect=center]
  encA2 = Pad [width=2.1630119375573931 height=3.8438016528925623 connect=center]
  SWp1 = Pad [width=2.5590406265296126 height=2.4458149779735674 connect=center]
  SWp2 = Pad [width=2.5590406265296126 height=2.4458149779735674 connect=center]
  C3 = Ceramic Capacitor [capacitance=2.2µF package="100 mil [THT, multilayer]"]

nets:
  N1: U1.RESET, YES-_R1.Pin_1
  encB1: U1.D2, encB1.pad
  encA1: U1.D3_(PWM), encA1.pad
  N2: U1.D4, LCD.pin14
  VCC: U1.VCC, YES-_R1.Pin_0, LCD.pin2, TRIMPOT.wiper, TRIMPOT1.leg2, VCC.pad, SWp2.pad, C3.1
  GND: U1.GND, C1.0, C2.0, D5_zero.Pin_3, D5_zero.Pin_4, D4_Polaris.Pin_3, D4_Polaris.Pin_4, A0_setAZI.Pin_3, A0_setAZI.Pin_4, A4_setALT.Pin_3, A4_setALT.Pin_4, LCD.pin1, LCD.pin5, LCD.pin7, LCD.pin8, LCD.pin9, LCD.pin10, LCD.pin16, encMan.pin2, encMan.pin3, TRIMPOT1.leg1, GND.pad, GND_2.pad, C3.0
  N3: U1.XLAT1, XTAL1.pin_0, C2.1
  N4: U1.XLAT2, XTAL1.pin_1, C1.1
  N5: U1.D5_(PWM), LCD.pin13
  N6: U1.D6_(PWM), LCD.pin12
  N7: U1.D7, LCD.pin11
  N8: U1.D9_(PWM), LCD.pin6
  N9: U1.D10_(PWM), LCD.pin4
  N10: U1.D11_(PWM), D5_zero.Pin_1, D5_zero.Pin_2
  N11: U1.D12, D4_Polaris.Pin_1, D4_Polaris.Pin_2
  N12: U1.D13, A0_setAZI.Pin_1, A0_setAZI.Pin_2
  N13: U1.A0, A4_setALT.Pin_1, A4_setALT.Pin_2
  N14: U1.A1, encMan.pin1
  N15: U1.A2, encMan_2.pin1
  N16: U1.A3, encMan_2.pin2
  encB2: U1.A4, encB2.pad
  encA2: U1.A5, encA2.pad
  N17: LCD.pin3, TRIMPOT1.wiper
  N18: LCD.pin15, TRIMPOT.leg2
  N19: BAT+.pad, SWp1.pad

notes:
  GP2 Orion Built wMods, GP2 Reflects built (except Cap), - A -
  1.   ADDED CAP TO STABALIZE VOLTAGE
