# Fritzing sketch id4037_GP2or_Nano1_0 (saved by Fritzing 0.9.3b)
breadboards: 1

parts:
  Part1 = Arduino Nano (Rev3.0)
  LCD1 = LCD screen
  0_0 = Momentary Switch [package=ksa_sealed_tac_switch]
  Polaris = Momentary Switch [package=ksa_sealed_tac_switch]
  Azi = Momentary Switch [package=ksa_sealed_tac_switch]
  Alt = Momentary Switch [package=ksa_sealed_tac_switch]
  Manual = Rotary Encoder [package=THT]
  Set = Momentary Switch [package=ksa_sealed_tac_switch]
  Azi_2 = Rotary Encoder [package=THT]
  Alt_2 = Rotary Encoder [package=THT]

nets:
  GND: Part1.GND, LCD1.VSS, LCD1.R/W, LCD1.DB0, LCD1.DB1, LCD1.DB2, LCD1.DB3, LCD1.LED-, 0_0.3, Polaris.3, Azi.3, Alt.3, Manual.EncoderPinC, Set.2, Azi_2.EncoderPinC, Alt_2.EncoderPinC
  N1: Part1.D2, Azi_2.EncoderPinA
  N2: Part1.D3, Alt_2.EncoderPinA
  N3: Part1.D4, LCD1.DB7
  N4: Part1.D5, LCD1.DB6
  N5: Part1.D6, LCD1.DB5
  N6: Part1.D7, LCD1.DB4
  N7: Part1.D9, LCD1.E
  N8: Part1.D10, LCD1.RS
  N9: Part1.D11/MOSI, 0_0.2
  N10: Part1.D12/MISO, Polaris.2
  5V: Part1.5V, LCD1.VDD
  N11: Part1.A5, Alt_2.EncoderPinB
  N12: Part1.A4, Azi_2.EncoderPinB
  N13: Part1.A3, Manual.EncoderPinB
  N14: Part1.A2, Manual.EncoderPinA
  N15: Part1.A1, Set.3
  N16: Part1.A0, Alt.2
  N17: Part1.D13/SCK, Azi.2

notes:
  Alt = 121.035 º
  Azi =  60.125 º
  The Manual Encoder and Btn Switch can be either individual or use an Encoder with a Btn Switch (press the shaft). You decide...
  Alt, Azi and Manual Encoder wiring depends on your brand of encoder - Be sure to check!
  The shown encoders do not have a Vcc input. They are ONLY for this graphic representation...
