# Fritzing sketch id4038_Voltage_and_Temp_Sensor_0 (saved by Fritzing 0.8.0b)
breadboards: 1

parts:
  DHT1 = DHT11_Temperature_and_Humitidy_Sensor
  Part1 = Arduino Pro Mini v13
  R1 = Resistor [tolerance=±5% resistance=4.7k package=THT]
  R2 = Resistor [tolerance=±5% resistance=15k package=THT]
  R3 = Resistor [tolerance=±5% resistance=330 package=THT]
  U1 = mystery part, 4 pins [chip_label="Polulu 3.3v"]
  J1 = screw terminal, 2 pins
  U2 = XBee

nets:
  VCC: DHT1.connector1, Part1.VCC, U1.pin4, U2.VCC
  N1: DHT1.connector2, Part1.A0
  GND: DHT1.connector4, Part1.GND, R1.Pin_1, U1.pin3, J1.pin1, U2.GND
  N2: Part1.A2, R1.Pin_0, R3.Pin_1
  N3: Part1.D1/RX, U2.pin3
  N4: Part1.D0/TX, U2.pin2
  N5: R2.Pin_0, R3.Pin_0
  N6: R2.Pin_1, U1.pin1, U1.pin2, J1.pin2

notes:
  12v
