# Fritzing sketch id4039_TEMP_HUM_DHT11_FR_0 (saved by Fritzing 0.9.3b)
breadboards: 1

parts:
  Composant1 = Arduino Uno (Rev3)
  R2 = Trimmer Potentiometer [maximum_resistance=10kΩ package=THT]  # not connected
  DHT1 = DHT11_Temperature_and_Humitidy_Sensor
  R3 = Rotary Potentiometer (Small) [maximum_resistance=100kΩ package=THT]
  R4 = Resistor [tolerance=±5% resistance=220 package=THT]
  LCD1 = LCD screen

nets:
  N1: Composant1.D8, DHT1.connector2, R4.Pin_0
  N2: Composant1.D11_PWM/MOSI, LCD1.E
  N3: Composant1.D12/MISO, LCD1.RS
  N4: Composant1.D2, LCD1.DB7
  N5: Composant1.D3_PWM, LCD1.DB6
  N6: Composant1.D4, LCD1.DB5
  N7: Composant1.D5_PWM, LCD1.DB4
  5V: Composant1.5V, LCD1.VDD, LCD1.LED+
  GND: Composant1.GND, LCD1.VSS, LCD1.R/W, LCD1.LED-
  N8: DHT1.connector1, R4.Pin_1
  N9: DHT1.connector4, R3.leg1, R3.leg2
  N10: R3.wiper, LCD1.V0
