# Fritzing sketch id403_Arduino_Baby_1_0 (saved by Fritzing 0.9.2b)
breadboards: 1

parts:
  LED1 = smd LED [color="Red (633nm)" package="0603 [SMD]"]
  LED2 = smd LED [color="Red (633nm)" package="0603 [SMD]"]
  LED3 = smd LED [color="Red (633nm)" package="0603 [SMD]"]
  R1 = Resistor [tolerance=±5% resistance=220 package="0603 [SMD]"]
  R2 = Resistor [tolerance=±5% resistance=220 package="0603 [SMD]"]
  R3 = Resistor [tolerance=±5% resistance=220 package="0603 [SMD]"]
  Componente1 = Arduino Uno (Rev3)
  LED4 = smd LED [color="Red (633nm)" package="0603 [SMD]"]
  R4 = Resistor [tolerance=±5% resistance=220 package="0603 [SMD]"]
  LED5 = smd LED [color="Red (633nm)" package="0603 [SMD]"]
  R5 = Resistor [tolerance=±5% resistance=220 package="0603 [SMD]"]

nets:
  N1: LED1.cathode, LED2.cathode, LED3.cathode, Componente1.GND, LED4.cathode, LED5.cathode
  N2: LED1.anode, R3.Pin_1
  N3: LED2.anode, R2.Pin_1
  N4: LED3.anode, R1.Pin_1
  N5: R1.Pin_0, Componente1.D4
  N6: R2.Pin_0, Componente1.D5_PWM
  N7: R3.Pin_0, Componente1.D6_PWM
  N8: Componente1.D2, R5.Pin_0
  N9: Componente1.D3_PWM, R4.Pin_0
  N10: LED4.anode, R4.Pin_1
  N11: LED5.anode, R5.Pin_1
