# Fritzing sketch id4040_Humidity_0 (saved by Fritzing 0.9.3b)
breadboards: 1

parts:
  Part1 = Arduino Uno (Rev3)
  RHT1 = Humidity and Temperature Sensor RHT03
  R1 = Resistor [tolerance=±5% resistance=4.7 package=THT]

nets:
  N1: Part1.D7, RHT1.Data-signal, R1.Pin_0
  5V: Part1.5V, RHT1.Vcc, R1.Pin_1
  N2: Part1.GND, RHT1.GND_2

notes:
  The Lcd With I2C
  Humidty : DHT11
