# Fritzing sketch id4042_TEMP_INTIAL_0 (saved by Fritzing 0.9.3b)
breadboards: 1

parts:
  Launchpad1 = TI Launchpad MSP430G2
  T1 = LM35 Temperature Sensor [package="TO92 [THT]"]
  Adafruit_HUZZAH_ESP8266_Breakout1 = Adafruit HUZZAH ESP8266 Breakout [part_number=2471]

nets:
  N1: Launchpad1.p2, T1.Vout
  N2: Launchpad1.p1, T1.+Vs
  GND: T1.GND, Adafruit_HUZZAH_ESP8266_Breakout1.GND

notes:
  This is not the same module as our wifi module ESP8266, but this is the closest repersentation we could find.
