# Fritzing sketch id4043_Untitled_Sketch_2_0 (saved by Fritzing 0.9.2b)
breadboards: 1

parts:
  Part1 = Arduino Uno (Rev3)
  T1 = TMP36 Temperature Sensor [package="TO92 [THT]"]
  R1 = Resistor [tolerance=±5% resistance=220 package="0805 [SMD]"]
  R2 = Resistor [tolerance=±5% resistance=220 package="0805 [SMD]"]
  R3 = Resistor [tolerance=±5% resistance=220 package="0805 [SMD]"]
  LED1 = smd LED [color="Red (633nm)" package="0603 [SMD]"]
  LED2 = smd LED [color="Red (633nm)" package="0603 [SMD]"]
  LED3 = smd LED [color="Red (633nm)" package="0603 [SMD]"]

nets:
  N1: Part1.A0, T1.Vout
  N2: Part1.D2, LED3.cathode
  N3: Part1.D3_PWM, LED2.cathode
  N4: Part1.D4, LED1.cathode
  GND: Part1.GND, T1.+Vs, T1.GND, R1.Pin_1, R2.Pin_1, R3.Pin_1
  N5: R1.Pin_0, LED1.anode
  N6: R2.Pin_0, LED2.anode
  N7: R3.Pin_0, LED3.anode
