# Fritzing sketch id4044_temp_0 (saved by Fritzing 0.9.0b)
breadboards: 1

parts:
  Part1 = Arduino Mega 2560 (Rev3)
  U1 = POT [package=pot_mammoth]
  T1 = LM35 Temperature Sensor [package="TO92 [THT]"]
  U2 = LCD-16X2 [package=lcd-16x2_noholes]
  R1 = Resistor [tolerance=±5% resistance=220 package="0603 [SMD]"]
  R2 = Resistor [package="0402 [SMD]"]

nets:
  GND: Part1.GND, U1.E, T1.GND, U2.VSS, U2.R_W
  N1: Part1.D12_PWM, U2.RS
  N2: Part1.D11_PWM, U2.E
  5V: Part1.5V, U2.VDD, U2.A, R1.Pin_0, R2.Pin_0
  N3: Part1.D2_PWM, U2.DB7
  N4: Part1.D3_PWM, U2.DB6
  N5: Part1.D4_PWM, U2.DB5
  N6: Part1.D5_PWM, U2.DB4
  N7: U1.A, U2.VO
  N8: T1.Vout, R2.Pin_1
  N9: U2.K, R1.Pin_1
