# Fritzing sketch id4045_Temp_Sensor_0 (saved by Fritzing 0.9.3b)
breadboards: 1

parts:
  Part1 = Arduino Uno (Rev3)
  U1 = TMP36 [package=to-92-kit]
  R1 = Resistor [tolerance=±5% resistance=220 package=THT]
  R2 = Resistor [tolerance=±5% resistance=220 package=THT]
  R3 = Resistor [tolerance=±5% resistance=220 package=THT]
  LED1 = RGB LED (com. anode, rbg) [package="5 mm [THT]"]

nets:
  N1: Part1.A0, U1.VOUT
  N2: Part1.D9_PWM, R1.Pin_0
  N3: Part1.D10_PWM/SS, R2.Pin_0
  N4: Part1.D11_PWM/MOSI, R3.Pin_0
  5V: Part1.5V, U1.VCC
  GND: Part1.GND, U1.GND, LED1.blue_cathode
  N5: R1.Pin_1, LED1.green_cathode
  N6: R2.Pin_1, LED1.common_anode
  N7: R3.Pin_1, LED1.red_cathode
