# Fritzing sketch id4046_temperatur_0 (saved by Fritzing 0.9.0b)
breadboards: 1

parts:
  LCD1 = LCD screen
  T1 = LM35 Temperature Sensor [package="TO92 [THT]"]
  Bauteil1 = Arduino Uno (Rev3)
  R1 = Rotary Potentiometer (Small) [maximum_resistance=100kΩ package=THT]
  R3 = Resistor [tolerance=±5% resistance=220 package=THT]
  R4 = Resistor [tolerance=±5% resistance=220 package=THT]
  R6 = Resistor [tolerance=±5% resistance=220 package=THT]
  R8 = Resistor [tolerance=±5% resistance=220 package=THT]
  LED2 = RGB LED (6 legs) [package="5 mm [THT]"]

nets:
  VSS: LCD1.VSS, LCD1.R/W, T1.Vout, Bauteil1.GND, R1.leg2
  VDD: LCD1.VDD, T1.+Vs, Bauteil1.5V, R1.leg1
  N1: LCD1.V0, R1.wiper
  N2: LCD1.RS, Bauteil1.D9_PWM
  N3: LCD1.E, Bauteil1.D8
  N4: LCD1.DB4, Bauteil1.D6_PWM
  N5: LCD1.DB5, Bauteil1.D5_PWM
  N6: LCD1.DB6, Bauteil1.D4
  N7: LCD1.DB7, Bauteil1.D3_PWM
  N8: T1.GND, Bauteil1.A5/SCL
  N9: Bauteil1.D10_PWM/SS, R6.Pin_0, R6.Pin_1, LED2.Blue2
  N10: Bauteil1.D11_PWM/MOSI, R8.Pin_0, R8.Pin_1, LED2.Red
  N11: Bauteil1.D12/MISO, R4.Pin_0, R4.Pin_1, LED2.Blue1
  N12: Bauteil1.D13/SCK, R3.Pin_0, R3.Pin_1, LED2.Green
