# Fritzing sketch id4047_thermometer_7segment_0 (saved by Fritzing 0.7.10b)
breadboards: 1

parts:
  T1 = LM35 Temperature Sensor [package="TO92 [THT]"]
  Arduino1 = Arduino
  R1 = Resistor [tolerance=±5% resistance=1k package=THT]
  7_Segment1 = 7 Segment Display
  7_Segment2 = 7 Segment Display
  S1 = Pushbutton [package=THT]
  R2 = Resistor [tolerance=±5% resistance=10k package=THT]
  LED1 = LED - 5mm [color="Red (633nm)" package="5 mm [THT]"]
  LED2 = LED - 5mm [color="Green (565nm)" package="5 mm [THT]"]
  R3 = Resistor [tolerance=±5% resistance=220 package=THT]
  R4 = Resistor [tolerance=±5% resistance=220 package=THT]

nets:
  N1: T1.+Vs, Arduino1.+5V, S1.leg0
  N2: T1.Vout, Arduino1.A0, R1.Pin_0
  GND: T1.GND, Arduino1.GND, R1.Pin_1, R2.Pin_0
  N3: Arduino1.D13, R3.Pin_0
  N4: Arduino1.D12, Arduino1.D11, 7_Segment1.common_anode, 7_Segment2.common_anode
  N5: Arduino1.D10, R4.Pin_0
  N6: Arduino1.D9, 7_Segment1.Segment_B, 7_Segment2.Segment_B
  N7: Arduino1.D8, 7_Segment1.Segment_A, 7_Segment2.Segment_A
  N8: Arduino1.D7, 7_Segment1.Segment_F, 7_Segment2.Segment_F
  N9: Arduino1.D6, 7_Segment1.Segment_G, 7_Segment2.Segment_G
  N10: Arduino1.D5, 7_Segment1.Segment_E, 7_Segment2.Segment_E
  N11: Arduino1.D4, 7_Segment1.Segment_D, 7_Segment2.Segment_D
  N12: Arduino1.D3, 7_Segment1.Segment_C, 7_Segment2.Segment_C
  N13: Arduino1.D2, 7_Segment1.Segment_DP, 7_Segment2.Segment_DP
  N14: Arduino1.A1, S1.leg1, R2.Pin_1
  N15: LED1.cathode, LED2.cathode
  N16: LED1.anode, R3.Pin_1
  N17: LED2.anode, R4.Pin_1
