# Fritzing sketch id404_Barometric_Pressure_Sensor_Breakout___BMP180_0 (saved by Fritzing 0.9.1b)
breadboards: 1

parts:
  Bauteil2 = Arduino Uno (Rev3) - ICSP
  Bauteil3 = Barometric Pressure Sensor - BMP085 Breakout

nets:
  N1: Bauteil2.A4/SDA, Bauteil3.SDA
  N2: Bauteil2.A5/SCL, Bauteil3.SCL
  3V3: Bauteil2.3V3, Bauteil3.VCC
  GND: Bauteil2.GND, Bauteil3.GND

notes:
  Barometric Pressure Sensor Breakout - BMP180
  - (GND) to GND
  + (VDD) to 3.3V
  Any Arduino pins labeled: SDA SCL
  ------------------------------------------------
  Uno, Redboard, Pro: A4 A5
  Mega2560, Due: 20 21
  Leonardo: 2 3
