# Fritzing sketch id4050_Temperatura_0 (saved by Fritzing 0.9.3b)
breadboards: 1

parts:
  Componente2 = Arduino Uno (Rev3) - ICSP  # not connected
  Componente3 = Arduino MicroSD Shield
  RHT1 = Humidity and Temperature Sensor RHT03
  Adafruit_HUZZAH_ESP8266_Breakout1 = Adafruit HUZZAH ESP8266 Breakout [part_number=2471]
  R1 = Resistor [tolerance=±5% resistance=220 package="0402 [SMD]"]
  R2 = Resistor [tolerance=±5% resistance=220 package="0402 [SMD]"]
  R3 = Resistor [tolerance=±5% resistance=220 package="0402 [SMD]"]
  R4 = Resistor [tolerance=±5% resistance=220 package="0402 [SMD]"]

nets:
  N1: Componente3.D3, Adafruit_HUZZAH_ESP8266_Breakout1.TX
  N2: Componente3.3.3V, Adafruit_HUZZAH_ESP8266_Breakout1.3V
  5V: Componente3.5V, RHT1.Vcc, R4.Pin_0
  N3: Componente3.D2, R2.Pin_0
  N4: Componente3.D7, RHT1.Data-signal, R4.Pin_1
  N5: Componente3.GND, RHT1.GND_2
  N6: Adafruit_HUZZAH_ESP8266_Breakout1.GND, R3.Pin_1
  N7: Adafruit_HUZZAH_ESP8266_Breakout1.RX, R1.Pin_0, R2.Pin_1
  N8: R1.Pin_1, R3.Pin_0
