# Fritzing sketch id4051_temperature_0 (saved by Fritzing 0.9.1b)
breadboards: 1

parts:
  Part1 = Arduino Uno (Rev3)
  LCD1 = LCD screen
  RHT1 = Humidity and Temperature Sensor RHT03
  R1 = Rotary Potentiometer (Small) [maximum_resistance=100kΩ package=THT]
  VCC1 = Battery block 9V

nets:
  N1: Part1.D11_PWM/MOSI, LCD1.E
  N2: Part1.D12/MISO, LCD1.RS
  N3: Part1.D2, LCD1.DB7
  N4: Part1.D3_PWM, LCD1.DB6
  N5: Part1.D4, LCD1.DB5
  N6: Part1.D5_PWM, LCD1.DB4
  5V: Part1.5V, LCD1.VDD, RHT1.Vcc, R1.leg1
  GND: Part1.GND, LCD1.VSS, LCD1.R/W, RHT1.GND_1, R1.leg2, VCC1.-
  N7: Part1.VIN, VCC1.+
  N8: LCD1.V0, R1.wiper
