# Fritzing sketch id4052_temp_hum_0 (saved by Fritzing 0.9.3b)
circuit board: 6.48997cm x 5.04852cm
breadboards: 1

parts:
  Part1 = Arduino Nano (Rev3.0)
  Part2 = BME280 Breakout
  8x8_LED_Modul_mit_MAX1 = 8x8 LED Modul mit MAX7219

nets:
  GND: Part1.GND, Part2.GND, 8x8_LED_Modul_mit_MAX1.connector1
  N1: Part1.D10, 8x8_LED_Modul_mit_MAX1.connector3
  N2: Part1.D11/MOSI, 8x8_LED_Modul_mit_MAX1.connector4
  N3: Part1.D12/MISO, 8x8_LED_Modul_mit_MAX1.connector2
  5V: Part1.5V, Part2.3.3V, 8x8_LED_Modul_mit_MAX1.connector0
  N4: Part1.A5, Part2.SCK/SCL
  N5: Part1.A4, Part2.SDI/SDA
