# Fritzing sketch id4053_dht11_read_fritzing_0 (saved by Fritzing 0.9.3b)

parts:
  Componente1 = Arduino Uno (Rev3)
  J1 = male pin header, 3 pins [form="♂ (male)"]

nets:
  N1: Componente1.D13/SCK, J1.pin1
  N2: Componente1.D7, J1.pin2
  N3: Componente1.5V, J1.pin3
