# Fritzing sketch id4054_Triple_Interface_0 (saved by Fritzing 0.9.3b)
breadboards: 1

parts:
  U2 = MPL3115A2 [package=lga8]
  Part1 = Arduino Uno (Rev3)
  U3 = MAX6675 [package=so08]
  R1 = Temperature Sensor (Thermistor) [thermistor_type=NTC package=THT]
  LCD1 = LCD screen
  R2 = Resistor [tolerance=±5% resistance=220 package="0805 [SMD]"]
  Part2 = LilyPad Arduino USB

nets:
  VDD: U2.VDD, Part1.5V, U3.VDD, LCD1.VDD, R2.Pin_0
  GND: U2.GND, Part1.GND, LCD1.VSS, LCD1.LED-, Part2.GND
  N1: U2.SDA, Part1.A4/SDA, Part2.A4
  N2: U2.SCL, Part1.A5/SCL, Part2.A5
  N3: Part1.A0, LCD1.V0
  N4: Part1.A2, Part2.A2
  N5: Part1.A3, Part2.A3
  N6: Part1.D9_PWM, U3.CS, Part2.D9
  N7: Part1.D10_PWM/SS, Part2.D10
  N8: Part1.D11_PWM/MOSI, LCD1.E, Part2.D11
  N9: Part1.D12/MISO, U3.MISO, LCD1.RS
  N10: Part1.D13/SCK, U3.SCK
  N11: Part1.D2, LCD1.DB7, Part2.D2
  N12: Part1.D3_PWM, LCD1.DB6, Part2.D3
  N13: Part1.D4, LCD1.DB5
  N14: Part1.D5_PWM, LCD1.DB4
  3V3: Part1.3V3, Part2.3V3
  N15: U3.T-, R1.pin_0
  N16: U3.T+, R1.pin_1
  N17: LCD1.LED+, R2.Pin_1

notes:
  Temperature Sensor(SPI Interfacing)
  Barometric Pressure Sensor(I2C interfacing)
  LCD Display (Analog interfacing)
  Arduino Lilypad(Communication Module)
