# Fritzing sketch id4056_Sketch_0 (saved by Fritzing 0.9.1b)
circuit board: 6.86876cm x 5.35391cm
breadboards: 1

parts:
  DHT22 = DHT22_Humidity_and_Temperature_Sensor
  R1 = Resistor [tolerance=±5% resistance=10k package=THT]
  Q1 = TRANSISTOR_NPN [package=to-92]
  R2 = Resistor [tolerance=±5% resistance=10k package=THT]
  Yun = Arduino Yun
  U1 = RELAY-2 [package=relay-g5v]  # not connected

nets:
  N1: DHT22.connector1, R1.Pin_1, Yun.5V
  N2: DHT22.connector2, R1.Pin_0, Yun.D4
  N3: DHT22.connector4, Q1.E, Yun.GND
  N4: Q1.B, R2.Pin_0
  N5: R2.Pin_1, Yun.D5_PWM
