# Fritzing sketch id4058_TempDisplay_0 (saved by Fritzing 0.9.1b)
breadboards: 1

parts:
  Part1 = Arduino Uno (Rev3)
  S1 = Pushbutton [package="[THT]"]
  T1 = LM35 Temperature Sensor [package="TO92 [THT]"]
  7_Segment_4_Digit_Display1 = MyPart1 [part_number=HS420561K-32]
  R1 = Resistor [tolerance=±5% resistance=220 package=THT]
  R2 = Resistor [tolerance=±5% resistance=220 package=THT]
  R3 = Resistor [tolerance=±5% resistance=220 package=THT]
  R4 = Resistor [tolerance=±5% resistance=220 package=THT]
  R5 = Resistor [tolerance=±5% resistance=220 package=THT]
  R6 = Resistor [tolerance=±5% resistance=220 package=THT]
  R7 = Resistor [tolerance=±5% resistance=220 package=THT]
  R8 = Resistor [tolerance=±5% resistance=220 package=THT]
  R9 = Resistor [tolerance=±5% resistance=10k package=THT]

nets:
  N1: Part1.A0, S1.Pin_1, S1.Pin_2, R9.Pin_1
  N2: Part1.A5/SCL, T1.Vout
  N3: Part1.D8, R8.Pin_0
  N4: Part1.D9_PWM, R7.Pin_0
  N5: Part1.D10_PWM/SS, R6.Pin_0
  N6: Part1.D12/MISO, R5.Pin_0
  N7: Part1.D0/RX, 7_Segment_4_Digit_Display1.connector12
  N8: Part1.D1/TX, 7_Segment_4_Digit_Display1.connector9
  N9: Part1.D2, 7_Segment_4_Digit_Display1.connector8
  N10: Part1.D3_PWM, 7_Segment_4_Digit_Display1.connector6
  N11: Part1.D4, R1.Pin_0
  N12: Part1.D5_PWM, R2.Pin_0
  N13: Part1.D6_PWM, R3.Pin_0
  N14: Part1.D7, R4.Pin_0
  N15: Part1.5V, S1.Pin_3, S1.Pin_4, T1.+Vs
  GND: Part1.GND, T1.GND, R9.Pin_0
  N16: 7_Segment_4_Digit_Display1.connector1, R8.Pin_1
  N17: 7_Segment_4_Digit_Display1.connector2, R7.Pin_1
  N18: 7_Segment_4_Digit_Display1.connector3, R5.Pin_1
  N19: 7_Segment_4_Digit_Display1.connector4, R6.Pin_1
  N20: 7_Segment_4_Digit_Display1.connector5, R4.Pin_1
  N21: 7_Segment_4_Digit_Display1.connector7, R3.Pin_1
  N22: 7_Segment_4_Digit_Display1.connector10, R1.Pin_1
  N23: 7_Segment_4_Digit_Display1.connector11, R2.Pin_1
