# Fritzing sketch id4059_DS18B20_temperature_0 (saved by Fritzing 0.9.3b)
circuit board: 8.46667cm x 5.64444cm
breadboards: 1

parts:
  Part1 = Arduino Uno (Rev3)
  R1 = Resistor [tolerance=±5% resistance=2.2k package=THT]
  Q1 = NPN-Transistor [package="SOT-23 [SMD]"]

nets:
  N1: Part1.GND, Q1.2
  N2: Part1.D2, R1.Pin_0, Q1.0
  N3: Part1.5V, R1.Pin_1, Q1.1
