# Fritzing sketch id405_AIO_Arduino_Based_Quadcopter_MainBoard_with_accelerometer_and_pdb_0 (saved by Fritzing 0.9.3b)
circuit board: 7cm x 7cm
breadboards: 1

parts:
  USB = female pin header, 6 pins [form="♀ (female)"]
  S1 = Pushbutton [package="[THT]"]
  16MHz = Crystal [frequency="16 Mhz" package=THT]
  C1 = Ceramic Capacitor [capacitance=100nF package="100 mil [THT, multilayer]"]
  C2 = Ceramic Capacitor [capacitance=100nF package="100 mil [THT, multilayer]"]
  R1 = Resistor [tolerance=±5% resistance=10k package=THT]
  C3 = Ceramic Capacitor [capacitance=100nF package="100 mil [THT, multilayer]"]
  LED = LED - 5mm [color="Red (633nm)" package="5 mm [THT]"]
  R2 = Resistor [tolerance=±5% resistance=220 package=THT]
  Power = female pin header, 2 pins [form="♀ (female)"]
  J5 = female pin header, 14 pins [form="♀ (female)"]
  J6 = female pin header, 14 pins [form="♀ (female)"]
  CPU = atmega168 [package=dip]
  ESC_4 = female pin header, 3 pins [form="♀ (female)"]
  ESC_3 = female pin header, 3 pins [form="♀ (female)"]
  ESC_2 = female pin header, 3 pins [form="♀ (female)"]
  ESC_1 = female pin header, 3 pins [form="♀ (female)"]
  BEC_+_- = female pin header, 2 pins [form="♀ (female)"]
  J14 = female pin header, 1 pin [form="♀ (female)"]
  R4 = Resistor [tolerance=±5% resistance=330 package=THT]
  LED1 = LED - 5mm [color="Red (633nm)" package="5 mm [THT]"]
  J7 = female pin header, 1 pin [form="♀ (female)"]
  Receiver_Outputs = female pin header, 4 pins [form="♀ (female)"]
  J8 = female pin header, 1 pin [form="♀ (female)"]
  J9 = female pin header, 1 pin [form="♀ (female)"]
  - = Pad [width=35 height=7 connect=center]
  + = Pad [width=35 height=7 connect=center]  # not connected
  GY2 = MPU-6050 GY-521 [form="♀ (female)"]

nets:
  N1: USB.pin1, S1.Pin_3, S1.Pin_4, C1.1, C2.1, LED.cathode, Power.pin2, J5.pin7, J6.pin8, CPU.GND
  N2: USB.pin3, R1.Pin_0, R2.Pin_1, Power.pin1, J5.pin9, J6.pin7, CPU.VCC, CPU.AVCC, GY2.connector0
  N3: USB.pin4, J6.pin2, CPU.D0_(RX)
  N4: USB.pin5, J6.pin3, CPU.D1_(TX)
  N5: USB.pin6, C3.0
  N6: S1.Pin_1, S1.Pin_2, R1.Pin_1, C3.1, J6.pin1, CPU.RESET
  N7: 16MHz.pin_0, C1.0, J6.pin9, CPU.XLAT1
  N8: 16MHz.pin_1, C2.0, J6.pin10, CPU.XLAT2
  N9: LED.anode, R2.Pin_0
  N10: J5.pin1, CPU.A5, GY2.connector2
  N11: J5.pin2, CPU.A4, GY2.connector3
  N12: J5.pin3, CPU.A3
  N13: J5.pin4, CPU.A2
  N14: J5.pin5, CPU.A1
  N15: J5.pin6, CPU.A0
  N16: J5.pin8, CPU.AREF
  N17: J5.pin10, CPU.D13
  N18: J5.pin11, CPU.D12, R4.Pin_0
  N19: J5.pin12, CPU.D11_(PWM), Receiver_Outputs.pin4
  N20: J5.pin13, CPU.D10_(PWM), Receiver_Outputs.pin3, J8.pin1
  N21: J5.pin14, CPU.D9_(PWM), Receiver_Outputs.pin2
  N22: J6.pin4, CPU.D2
  N23: J6.pin5, CPU.D3_(PWM)
  N24: J6.pin6, CPU.D4, ESC_1.pin1
  N25: J6.pin11, CPU.D5_(PWM), ESC_2.pin1, J9.pin1
  N26: J6.pin12, CPU.D6_(PWM), ESC_3.pin1
  N27: J6.pin13, CPU.D7, ESC_4.pin1
  N28: J6.pin14, CPU.D8, J7.pin1, Receiver_Outputs.pin1
  N29: ESC_4.pin3, ESC_3.pin3, ESC_2.pin3, ESC_1.pin3, LED1.cathode
  N30: BEC_+_-.pin1, -.pad, GY2.connector1
  N31: BEC_+_-.pin2, J14.pin1
  N32: R4.Pin_1, LED1.anode
