# Fritzing sketch id4060_Sketch_0 (saved by Fritzing 0.9.2b)
breadboards: 1

parts:
  Часть1 = Arduino Nano (Rev3.0)
  R1 = Resistor [tolerance=±5% resistance=10k package=THT]
  DHT1 = DHT11_Temperature_and_Humitidy_Sensor
  Nokia_5110_LCD_Module1 = Nokia5110LCDModule

nets:
  N1: Часть1.GND, DHT1.connector4, Nokia_5110_LCD_Module1.connector7
  N2: Часть1.D3, Nokia_5110_LCD_Module1.connector0
  N3: Часть1.D4, Nokia_5110_LCD_Module1.connector1
  N4: Часть1.D5, Nokia_5110_LCD_Module1.connector2
  N5: Часть1.D6, Nokia_5110_LCD_Module1.connector3
  N6: Часть1.D7, Nokia_5110_LCD_Module1.connector4
  N7: Часть1.D8, R1.Pin_0, DHT1.connector2
  N8: Часть1.5V, R1.Pin_1, DHT1.connector1
  N9: Часть1.3V3, Nokia_5110_LCD_Module1.connector5, Nokia_5110_LCD_Module1.connector6
