# Fritzing sketch id4061_DHT22_LCD_Serial_0 (saved by Fritzing 0.7.1b)
breadboards: 1

parts:
  Arduino1 = Arduino
  R1 = Trimmer Potentiometer [maximum_resistance=10kΩ package=THT]
  RHT1 = Humidity and Temperature Sensor RHT03 [part_number="SHT15 Breakout Board"]
  LCD1 = LCD screen  # not connected
  R2 = Resistor [tolerance=±5% resistance=10 package=THT]  # not connected

nets:
  N1: Arduino1.D6, RHT1.Data-signal
  +5V: Arduino1.+5V, R1.leg1, RHT1.Vcc
  N2: Arduino1.GND, R1.leg2, RHT1.GND_2
