# Fritzing sketch id4062_Temperature_logger_0 (saved by Fritzing 0.9.3b)
circuit board: 8.46667cm x 5.64444cm
breadboards: 1

parts:
  Composant1 = Arduino Nano (Rev3.0)
  Composant2 = MicroSD Card Module
  R1 = Resistor [tolerance=±5% resistance=47k package=THT]
  U1 = SWITCH-SPST-2 [package=r_sw_th]
  U2 = LIPO-2000mAh [package=lipo-2000]
  DS3 = DS18B20 1-Wire Temperature Sensor [part_number=DS18B20]
  DS2 = DS18B20 1-Wire Temperature Sensor [part_number=DS18B20]
  R2 = Resistor [tolerance=±5% resistance=220 package=THT]
  LED1 = smd LED [color="Red (633nm)" package="0805 [SMD]"]

nets:
  GND: Composant1.GND, Composant2.GND, U2.-, DS3.GND, DS2.GND, LED1.cathode
  N1: Composant1.D2, R1.Pin_1, DS3.DQ, DS2.DQ
  N2: Composant1.D4, Composant2.CS
  N3: Composant1.D7, R2.Pin_1
  N4: Composant1.D11/MOSI, Composant2.MOSI
  N5: Composant1.D12/MISO, Composant2.MISO
  N6: Composant1.VIN, U1.P
  VDD: Composant1.5V, Composant2.VCC, R1.Pin_0, DS3.VDD, DS2.VDD
  N7: Composant1.D13/SCK, Composant2.SCK
  N8: U1.O, U2.+
  N9: R2.Pin_0, LED1.anode
