# Fritzing sketch id4063_lcd_buzzer_temperatura_0 (saved by Fritzing 0.9.0b)
breadboards: 1

parts:
  LCD1 = LCD screen
  S1 = Pushbutton [package="[THT]"]
  Parte1 = Arduino Uno (Rev3)
  J1 = Piezo Speaker
  RHT1 = Humidity and Temperature Sensor RHT03
  R1 = Resistor [tolerance=±5% resistance=10k package="0603 [SMD]"]
  R2 = Resistor [tolerance=±5% resistance=10k package="0603 [SMD]"]
  R3 = Rotary Potentiometer (Large) [package=THT]

nets:
  VSS: LCD1.VSS, LCD1.R/W, LCD1.LED-, Parte1.GND, J1.pin2, RHT1.GND_2, R2.Pin_1, R3.leg1, R3.leg2
  VDD: LCD1.VDD, LCD1.LED+, S1.Pin_3, S1.Pin_4, Parte1.5V, RHT1.Vcc, R1.Pin_1
  N1: LCD1.V0, R3.wiper
  N2: LCD1.RS, Parte1.D12/MISO
  N3: LCD1.E, Parte1.D11_PWM/MOSI
  N4: LCD1.DB4, Parte1.D5_PWM
  N5: LCD1.DB5, Parte1.D4
  N6: LCD1.DB6, Parte1.D3_PWM
  N7: LCD1.DB7, Parte1.D2
  N8: S1.Pin_1, S1.Pin_2, Parte1.D8, R2.Pin_0
  N9: Parte1.D10_PWM/SS, J1.pin1
  N10: Parte1.D7, RHT1.Data-signal, R1.Pin_0
