# Fritzing sketch id4064_Untitled_Sketch_0 (saved by Fritzing 0.9.3b)
breadboards: 1

parts:
  Composant1 = Arduino Uno (Rev3)
  T1 = LM35 Temperature Sensor [package="TO92 [THT]"]
  R1 = Trimmer Potentiometer [maximum_resistance=10kΩ package=THT]
  LCD1 = LCD screen

nets:
  N1: Composant1.A0, T1.Vout
  N2: Composant1.D10_PWM/SS, LCD1.E
  N3: Composant1.D11_PWM/MOSI, LCD1.RS
  N4: Composant1.D1/TX, LCD1.DB7
  N5: Composant1.D2, LCD1.DB6
  N6: Composant1.D3_PWM, LCD1.DB5
  N7: Composant1.D4, LCD1.DB4
  N8: T1.+Vs, R1.leg2, LCD1.VDD
  GND: T1.GND, R1.leg1, LCD1.VSS, LCD1.R/W
  N9: R1.wiper, LCD1.V0
