# Fritzing sketch id4065_LM35_with_LCD_0 (saved by Fritzing 0.7.1b)
breadboards: 1

parts:
  Arduino1 = Arduino
  LCD1 = LCD screen
  R1 = Rotary Potentiometer (Small) [maximum_resistance=5kΩ]
  T1 = LM35 Temperature Sensor [package="TO92 [THT]"]

nets:
  GND: Arduino1.GND, LCD1.VSS, LCD1.R/W, LCD1.LED-, R1.leg1, T1.GND
  N1: Arduino1.D12, LCD1.RS
  N2: Arduino1.D11, LCD1.E
  N3: Arduino1.D5, LCD1.DB4
  N4: Arduino1.D4, LCD1.DB5
  N5: Arduino1.D3, LCD1.DB6
  N6: Arduino1.D2, LCD1.DB7
  +5V: Arduino1.+5V, LCD1.VDD, LCD1.LED+, R1.leg2, T1.+Vs
  N7: Arduino1.A0, T1.Vout
  N8: LCD1.V0, R1.wiper

notes:
  /*
  lm35 sketch
  prints the temperature to LCD
  */
  #include <LiquidCrystal.h>
  LiquidCrystal lcd(12, 11, 5, 4, 3, 2);
  const int inPin = 0;
  void setup()
  {
  lcd.begin(16, 2);
  }
  void loop()
  {
  int value = analogRead(inPin);
  lcd.setCursor(0, 1);
  float millivolts = (value / 1024.0) * 5000;
  float celsius = millivolts / 10;
  lcd.clear();
  lcd.setCursor(0,0);
  lcd.print(celsius);
  lcd.print(" Celsius");
  lcd.setCursor(0,1);
  lcd.print((celsius * 9)/ 5 + 32);
  lcd.print(" Fahrenheit");
  delay(10000);
  }
