# Fritzing sketch id4066_motorfan_0 (saved by Fritzing 0.9.2b)
breadboards: 1

parts:
  Part1 = Arduino Uno (Rev3)
  U1 = TMP36 [package=to-92]
  M1 = DC Motor
  Q1 = TRANSISTOR_PNP [package=to-92]

nets:
  N1: Part1.A0, U1.VOUT
  N2: Part1.D8, M1.pin_2
  5V: Part1.5V, U1.VCC, Q1.E
  GND: Part1.GND, U1.GND, M1.pin_1, Q1.C
