# Fritzing sketch id4069_LM35_Temperature_Sensor_0 (saved by Fritzing 0.9.0b)
breadboards: 1

parts:
  Componente1 = Arduino Uno (Rev3) - ICSP
  T1 = LM35 Temperature Sensor [package="TO92 [THT]"]

nets:
  N1: Componente1.A1, T1.Vout
  N2: Componente1.5V, T1.+Vs
  GND: Componente1.GND, T1.GND
