# Fritzing sketch id4070_Temperature_LED_Display_0 (saved by Fritzing 0.9.2b)
breadboards: 1

parts:
  Part1 = Arduino Uno (Rev3)
  LED4 = LED - 5mm [color="White (8000K)" package="5 mm [THT]"]
  LED3 = LED - 5mm [color="Red (633nm)" package="5 mm [THT]"]
  LED2 = LED - 5mm [color="Green (555nm)" package="5 mm [THT]"]
  LED2_2 = LED - 5mm [color="Blue (470nm)" package="5 mm [THT]"]
  U1 = TMP36 [package=to-92-kit]
  R1 = Resistor [tolerance=±5% resistance=560 package=THT]
  R2 = Resistor [tolerance=±5% resistance=560 package=THT]
  R3 = Resistor [tolerance=±5% resistance=560 package=THT]
  R4 = Resistor [tolerance=±5% resistance=560 package=THT]

nets:
  N1: Part1.A0, U1.VOUT
  N2: Part1.D10_PWM/SS, LED3.anode
  N3: Part1.D11_PWM/MOSI, LED2.anode
  N4: Part1.D12/MISO, LED2_2.anode
  N5: Part1.D13/SCK, LED4.anode
  5V: Part1.5V, U1.VCC
  GND: Part1.GND, U1.GND, R1.Pin_0, R2.Pin_0, R3.Pin_0, R4.Pin_0
  N6: LED4.cathode, R1.Pin_1
  N7: LED3.cathode, R2.Pin_1
  N8: LED2.cathode, R3.Pin_1
  N9: LED2_2.cathode, R4.Pin_1
