# Fritzing sketch id4071_TMP102_0 (saved by Fritzing 0.7.1b)

parts:
  Arduino1 = Arduino
  Part1 = Digital Temperature Sensor Breakout - TMP102

nets:
  N1: Arduino1.3V3, Part1.V+
  GND: Arduino1.GND, Part1.GND, Part1.ADD0
  N2: Arduino1.A4, Part1.SDA
  N3: Arduino1.A5, Part1.SCL
