# Fritzing sketch id4072_NimbitsTemp_0 (saved by Fritzing 0.7.11b)
breadboards: 1

parts:
  Arduino1 = Arduino  # not connected
  Arduino_Ethernet_Shield1 = Arduino Ethernet Shield
  LED1 = LED - 5mm [color="Red (633nm)" package="5 mm [THT]"]
  LED2 = LED - 5mm [color="Green (560nm)" package="5 mm [THT]"]
  LED3 = LED - 5mm [color="Yellow (592nm)" package="5 mm [THT]"]
  R1 = Resistor [tolerance=±5% resistance=220 package=THT]
  R2 = Resistor [tolerance=±5% resistance=220 package=THT]
  R3 = Resistor [tolerance=±5% resistance=220 package=THT]
  R4 = Resistor [tolerance=±5% resistance=220 package=THT]
  T1 = LM35 Temperature Sensor [package="TO92 [THT]"]

nets:
  N1: Arduino_Ethernet_Shield1.SS, R1.Pin_1
  N2: Arduino_Ethernet_Shield1.D3, R2.Pin_1
  N3: Arduino_Ethernet_Shield1.D2, R3.Pin_1
  N4: Arduino_Ethernet_Shield1.+5V, R4.Pin_0
  GND: Arduino_Ethernet_Shield1.GND, LED1.cathode, LED2.cathode, LED3.cathode, T1.GND
  N5: Arduino_Ethernet_Shield1.A5, R4.Pin_1, T1.Vout
  N6: LED1.anode, R2.Pin_0
  N7: LED2.anode, R3.Pin_0
  N8: LED3.anode, R1.Pin_0
