# Fritzing sketch id4073_ARM_LM35_v1_0 (saved by Fritzing 0.9.2b)
breadboards: 1

parts:
  T1 = LM35 Temperature Sensor [package="TO92 [THT]"]
  Launchpad1 = EK-TM4C123GXL_v0

nets:
  N1: T1.+Vs, Launchpad1.connector43
  N2: T1.Vout, Launchpad1.connector27
  N3: T1.GND, Launchpad1.connector45
