# Fritzing sketch id4074_Temp_0 (saved by Fritzing 0.9.2b)
breadboards: 1

parts:
  Bauteil1 = Arduino Uno (Rev3)
  LCD1 = LCD screen
  R1 = Trimmer Potentiometer [maximum_resistance=10kΩ package=THT]
  R2 = Resistor [tolerance=±5% resistance=220 package=THT]
  R3 = Temperature Sensor (Thermistor) [thermistor_type=NTC package=THT]
  R4 = Resistor [tolerance=±5% resistance=220 package=THT]  # not connected
  R5 = Resistor [tolerance=±5% resistance=220 package=THT]
  LED1 = LED - 5mm [color="Green (570nm)" package="5 mm [THT]"]
  LED2 = LED - 5mm [color="Yellow (595nm)" package="5 mm [THT]"]
  LED3 = LED - 5mm [color="Red (633nm)" package="5 mm [THT]"]
  R6 = Resistor [tolerance=±5% resistance=220 package=THT]
  R7 = Resistor [tolerance=±5% resistance=220 package=THT]
  R8 = Resistor [tolerance=±5% resistance=220 package=THT]

nets:
  N1: Bauteil1.A0, R3.pin_1, R5.Pin_0
  N2: Bauteil1.D11_PWM/MOSI, R8.Pin_0
  N3: Bauteil1.D12/MISO, R7.Pin_0
  N4: Bauteil1.D13/SCK, R6.Pin_0
  N5: Bauteil1.D2, LCD1.DB7
  N6: Bauteil1.D3_PWM, LCD1.DB6
  N7: Bauteil1.D4, LCD1.DB5
  N8: Bauteil1.D5_PWM, LCD1.DB4
  N9: Bauteil1.D6_PWM, LCD1.DB0
  N10: Bauteil1.D7, LCD1.RS
  5V: Bauteil1.5V, LCD1.VDD, R1.leg1, R2.Pin_0, R5.Pin_1
  GND: Bauteil1.GND, LCD1.VSS, LCD1.R/W, LCD1.LED-, R1.leg2, R3.pin_0, LED1.cathode, LED2.cathode, LED3.cathode
  N11: LCD1.V0, R1.wiper
  N12: LCD1.LED+, R2.Pin_1
  N13: LED1.anode, R8.Pin_1
  N14: LED2.anode, R7.Pin_1
  N15: LED3.anode, R6.Pin_1
