# Fritzing sketch id4075_Untitled_Sketch_0 (saved by Fritzing 0.8.5b)
breadboards: 1

parts:
  Part1 = Arduino Uno (Rev3)
  T1 = LM35 Temperature Sensor [package="TO92 [THT]"]
  M1 = DC Motor
  R3 = TRIMPOT [package=trimpot_pth_s3_lock]
  J1 = Piezo Speaker
  R4 = Resistor [tolerance=±5% resistance=220 package=THT]
  LCD1 = LCD screen

nets:
  N1: Part1.A1, T1.Vout
  N2: Part1.D9_PWM, M1.pin_2, J1.pin2
  N3: Part1.D11_PWM/MOSI, LCD1.E
  N4: Part1.D12/MISO, LCD1.RS
  GND: Part1.GND, T1.GND, R3.CCW, LCD1.VSS, LCD1.R/W, LCD1.LED-
  N5: Part1.D2, R3.WIPER, LCD1.V0, LCD1.DB7
  N6: Part1.D3_PWM, LCD1.DB6
  N7: Part1.D4, LCD1.DB5
  N8: Part1.D5_PWM, LCD1.DB4
  5V: Part1.5V, T1.+Vs, M1.pin_1, R3.CW, J1.pin1, R4.Pin_1, LCD1.VDD
  N9: R4.Pin_0, LCD1.LED+
