# Fritzing sketch id4076_tempescope_0 (saved by Fritzing 0.7.10b)
breadboards: 3

parts:
  24VIn = Screw terminal - 2 pins [package=THT]
  C2 = Electrolytic Capacitor [capacitance=2.2µF voltage=50V package="100 mil [THT, electrolytic]"]  # not connected
  aaa = IC, DIP package, 4 pins [chip_label=941H-2C-5D]
  Mist = Screw terminal - 2 pins [package=THT]
  U1 = atmega328 [package=dip]
  IC1 = IC, DIP package, 4 pins [chip_label=HPH03001]
  R1 = Resistor [tolerance=±5% resistance=220 package=THT]
  R2 = Resistor [tolerance=±5% resistance=220 package=THT]
  C3 = Electrolytic Capacitor [capacitance=2.2µF voltage=50V package="100 mil [THT, electrolytic]"]
  Q1 = NPN-Transistor [part_number=SC1815 package="TO92 [THT]"]
  Water_Pump = Screw terminal - 2 pins [package=THT]
  D1 = Rectifier Diode [part_number=1N4001 package="300 mil [THT]"]
  R3 = Resistor [tolerance=±5% resistance=10k package=THT]
  R4 = Resistor [tolerance=±5% resistance=150 package=THT]
  Q2 = Basic FET P-Channel [package="TO220 [THT]"]
  C4 = Electrolytic Capacitor [capacitance=100nF package="100 mil [THT, electrolytic]"]
  Y1 = Resonator [frequency="16 Mhz" package=THT]
  IC2 = IC, DIP package, 16 pins [chip_label=TD62003AP]  # not connected
  LED1 = RGB LED (com. anode, rbg) [package="5 mm [THT]"]
  Water_Pump1 = Screw terminal - 2 pins [package=THT]
  IC3 = IC, DIP package, 4 pins [chip_label=RX part_number=RX315-ZR4]

nets:
  N1: 24VIn.pin1, aaa.pin1, U1.GND#7, U1.A0, IC1.pin4, R1.Pin_0, R2.Pin_0, C3.-, Q1.E, R3.Pin_0, Q2.drain, C4.-, Y1.GND, IC3.pin1
  N2: 24VIn.pin2, Mist.pin1, IC1.pin3
  N3: aaa.pin2, U1.D2
  N4: aaa.pin3, U1.AREF, U1.GND#21, Q2.source, C4.+, LED1.common_anode, Water_Pump1.pin1, IC3.pin4
  N5: aaa.pin4, Mist.pin2
  N6: U1.XLAT1, Y1.0
  N7: U1.XLAT2, Y1.pin_1
  N8: U1.D8, IC3.pin2
  N9: U1.D13, R4.Pin_1
  N10: IC1.pin1, R1.Pin_1, R2.Pin_1
  N11: IC1.pin2, C3.+, Water_Pump.pin1, D1.cathode, Q2.gate
  N12: Q1.B, Water_Pump.pin2, D1.anode
  N13: Q1.C, R3.Pin_1, R4.Pin_0

notes:
  24V Area
  7V Area
  5V Area
  To the mist maker
  To the water pump
  To Fan
  RGB LED
  Tempescope Schematics 1.0.0 2013/6/9
  Ken Kawamoto
  ken@kawamoto.co.uk
  Released under Creative Commons Attribution-ShareAlike 3.0a
