# Fritzing sketch id4078_TmpBar_0 (saved by Fritzing 0.7.4b)
breadboards: 1

parts:
  LED1 = LED - 5mm [color="Yellow (595nm)" package="5 mm [THT]"]
  R1 = Resistor [tolerance=±5% resistance=330 package=THT]
  R2 = Resistor [tolerance=±5% resistance=330 package=THT]
  R3 = Resistor [tolerance=±5% resistance=330 package=THT]
  R4 = Resistor [tolerance=±5% resistance=330 package=THT]
  R5 = Resistor [tolerance=±5% resistance=330 package=THT]
  R6 = Resistor [tolerance=±5% resistance=330 package=THT]
  R7 = Resistor [tolerance=±5% resistance=330 package=THT]
  R8 = Resistor [tolerance=±5% resistance=330 package=THT]
  R9 = Resistor [tolerance=±5% resistance=330 package=THT]
  T1 = TMP36 Temperature Sensor [package="TO92 [THT]"]
  LED3 = LED - 5mm [color="Yellow (595nm)" package="5 mm [THT]"]
  LED5 = LED - 5mm [color="Yellow (595nm)" package="5 mm [THT]"]
  LED6 = LED - 5mm [color="Yellow (595nm)" package="5 mm [THT]"]
  LED7 = LED - 5mm [color="Yellow (595nm)" package="5 mm [THT]"]
  LED8 = LED - 5mm [color="Yellow (595nm)" package="5 mm [THT]"]
  LED9 = LED - 5mm [color="Yellow (595nm)" package="5 mm [THT]"]
  LED10 = LED - 5mm [color="Yellow (595nm)" package="5 mm [THT]"]
  LED11 = LED - 5mm [color="Yellow (595nm)" package="5 mm [THT]"]
  Arduino1 = Arduino

nets:
  N1: LED1.cathode, Arduino1.D2
  N2: LED1.anode, R9.Pin_1
  GND: R1.Pin_0, R2.Pin_0, R3.Pin_0, R4.Pin_0, R5.Pin_0, R6.Pin_0, R7.Pin_0, R8.Pin_0, R9.Pin_0, T1.GND, Arduino1.GND
  N3: R1.Pin_1, LED3.anode
  N4: R2.Pin_1, LED11.anode
  N5: R3.Pin_1, LED10.anode
  N6: R4.Pin_1, LED9.anode
  N7: R5.Pin_1, LED8.anode
  N8: R6.Pin_1, LED7.anode
  N9: R7.Pin_1, LED6.anode
  N10: R8.Pin_1, LED5.anode
  N11: T1.+Vs, Arduino1.aref, Arduino1.3V3
  N12: T1.Vout, Arduino1.A0
  N13: LED3.cathode, Arduino1.D3
  N14: LED5.cathode, Arduino1.D10
  N15: LED6.cathode, Arduino1.D9
  N16: LED7.cathode, Arduino1.D8
  N17: LED8.cathode, Arduino1.D7
  N18: LED9.cathode, Arduino1.D6
  N19: LED10.cathode, Arduino1.D5
  N20: LED11.cathode, Arduino1.D4
