# Fritzing sketch id4079_ambient_light_sensor_0 (saved by Fritzing 0.9.1b)
breadboards: 1

parts:
  Part1 = Arduino Pro Mini v13
  Part2 = Ambient Light Sensor (TEMT6000 Breakout Board)
  VCC1 = 4 x AAA Battery Mount

nets:
  VCC: Part1.VCC, Part2.VCC, VCC1.+
  GND: Part1.GND, Part2.GND, VCC1.-
  N1: Part1.A0, Part2.S

notes:
  https://anasdalintakam.blogspot.in/
