# Fritzing sketch id407_xxxxxxxxxxxxxxxxxxx_0 (saved by Fritzing 0.9.3b)
breadboards: 1

parts:
  Part1 = Digital FM Radio Receiver
  Part2 = Arduino Uno (Rev3)
  U1 = LCD-16X2 [package=lcd-16x2_noholes]
  R1 = Trimmer Potentiometer [maximum_resistance=10kΩ package=THT]
  SP1 = SPEAKER [package=pcb_mount_speaker]  # not connected
  SP2 = SPEAKER [package=pcb_mount_speaker]  # not connected
  R2 = Resistor [tolerance=±5% resistance=220 package="1206 [SMD]"]

nets:
  N1: Part1.!SEN, Part1.SCLK, Part2.A5/SCL
  N2: Part1.SDIO, Part2.A4/SDA
  GND: Part1.GND, Part2.GND, U1.VSS, U1.R_W, R1.leg2, R2.Pin_0
  3.3V: Part1.3.3V, Part2.3V3
  N3: Part2.D11_PWM/MOSI, U1.E
  N4: Part2.D12/MISO, U1.RS
  N5: Part2.D2, U1.DB7
  N6: Part2.D3_PWM, U1.DB6
  N7: Part2.D4, U1.DB5
  N8: Part2.D5_PWM, U1.DB4
  5V: Part2.5V, U1.VDD, U1.A, R1.leg1
  N9: U1.VO, R1.wiper
  N10: U1.K, R2.Pin_1
