# Fritzing sketch id4080_Servo1 (saved by Fritzing 0.9.3b)
breadboards: 1

parts:
  S1 = Pushbutton [package="[THT]"]
  Part1 = Arduino Uno (Rev3)
  J1 = Basic Servo

nets:
  N1: S1.Pin_1, S1.Pin_2, J1.vcc
  N2: S1.Pin_3, S1.Pin_4, Part1.5V
  N3: Part1.D9_PWM, J1.pulse
  GND: Part1.GND, J1.gnd
