# Fritzing sketch id4080_tennis_for_two_0 (saved by Fritzing 0.7.12b)
breadboards: 1

parts:
  R1 = Rotary Potentiometer (Small) [maximum_resistance=100kΩ]
  S1 = Pushbutton [package="[THT]"]
  R2 = Rotary Potentiometer (Small) [maximum_resistance=100kΩ]
  S2 = Pushbutton [package="[THT]"]
  R3 = Resistor [tolerance=±5% resistance=100 package=THT]
  R4 = Resistor [tolerance=±5% resistance=100 package=THT]
  WiringS1 = Wiring S [part_number="Wiring S"]

nets:
  N1: R1.leg1, R2.leg1, WiringS1.5V
  N2: R1.wiper, WiringS1.D25
  N3: R1.leg2, R2.leg2, R3.Pin_1, R4.Pin_0, WiringS1.GND
  N4: S1.Pin_1, S1.Pin_2, R3.Pin_0
  N5: S1.Pin_3, S1.Pin_4, WiringS1.D22
  N6: R2.wiper, WiringS1.D24
  N7: S2.Pin_1, S2.Pin_2, WiringS1.D23
  N8: S2.Pin_3, S2.Pin_4, R4.Pin_1
