# Fritzing sketch id4083_Termometr_1_0 (saved by Fritzing 0.8.7b)
breadboards: 1

parts:
  Part1 = Arduino Uno (Rev3)
  U1 = LCD-16X2 [package=lcd-16x2]
  S1 = Pushbutton [package="[THT]"]
  LED1 = smd LED [color="Yellow (595nm)" package="0805 [SMD]"]
  U2 = POT [package=pot_mammoth]
  R1 = Resistor [tolerance=±5% resistance=10k package=THT]
  R2 = Resistor [tolerance=±5% resistance=10k package=THT]
  R3 = Resistor [tolerance=±5% resistance=220 package=THT]
  T1 = LM35 Temperature Sensor [part_number=MCP9700A package="TO92 [THT]"]

nets:
  N1: Part1.A0, T1.Vout
  N2: Part1.D8, R3.Pin_1
  N3: Part1.D11_PWM/MOSI, U1.E
  N4: Part1.D12/MISO, U1.RS
  N5: Part1.D13/SCK, LED1.anode
  N6: Part1.D2, U1.DB7
  N7: Part1.D3_PWM, U1.DB6
  N8: Part1.D4, U1.DB5
  N9: Part1.D5_PWM, U1.DB4
  5V: Part1.5V, U1.VDD, U2.E, R2.Pin_1, T1.+Vs
  GND: Part1.GND, U1.VSS, U1.R_W, S1.Pin_3, S1.Pin_4, U2.S, T1.GND
  N10: U1.VO, U2.A
  N11: S1.Pin_1, S1.Pin_2, R2.Pin_0, R3.Pin_0
  N12: LED1.cathode, R1.Pin_1
