# Fritzing sketch id4084_TErmometro_0 (saved by Fritzing 0.9.1b)
circuit board: 8.46667cm x 5.64444cm
breadboards: 1

parts:
  Arduino_UNO = Arduino Uno (Rev3)
  T1 = TMP36 Temperature Sensor [package="TO92 [THT]"]
  R1 = Rotary Potentiometer (Small) [maximum_resistance=100kΩ package=THT]
  LCD1 = LCD screen
  R2 = Resistor [tolerance=±5% resistance=220 package=THT]
  C1 = Electrolytic Capacitor [capacitance=1µF package="100 mil [THT, electrolytic]"]

nets:
  N1: Arduino_UNO.A0, T1.Vout
  N2: Arduino_UNO.D11_PWM/MOSI, LCD1.E
  N3: Arduino_UNO.D12/MISO, LCD1.RS
  GND: Arduino_UNO.GND, T1.GND, R1.leg2, LCD1.VSS, LCD1.R/W, LCD1.LED-, C1.-
  N4: Arduino_UNO.D2, LCD1.DB7
  N5: Arduino_UNO.D3_PWM, LCD1.DB6
  N6: Arduino_UNO.D4, LCD1.DB5
  N7: Arduino_UNO.D5_PWM, LCD1.DB4
  5V: Arduino_UNO.5V, T1.+Vs, R1.leg1, LCD1.VDD, R2.Pin_1, C1.+
  N8: R1.wiper, LCD1.V0
  N9: LCD1.LED+, R2.Pin_0
