# Fritzing sketch id4087_Projeto_Alpha_0 (saved by Fritzing 0.9.3b)
circuit board: 2.15312cm x 3.07121cm
breadboards: 1

parts:
  U1 = ESP8266 ESP-01 Upgraded Version [part_number=ESP8266]
  R1 = Resistor [tolerance=±5% resistance=4.7k package="2010 [SMD]"]
  U2 = LIPO-2000mAh [package=lipo-2000]
  DS1 = DS18B20 1-Wire Temperature Sensor [part_number=DS18B20]

nets:
  N1: U1.connector1, R1.Pin_0, U2.+, DS1.VDD
  N2: U1.connector4, R1.Pin_1, DS1.DQ
  N3: U1.connector6, U2.-, DS1.GND
