# Fritzing sketch id4088_LCD_NOKIA_5110_teste_0 (saved by Fritzing 0.8.7b)
breadboards: 1

parts:
  U1 = DISPLAY NOKIA 5110
  S1 = Pushbutton [package="[THT]"]
  R1 = Temperature Sensor (Thermistor) [thermistor_type=NTC package=THT]
  R2 = Resistor [tolerance=±5% resistance=220 package=THT]
  R3 = Resistor [tolerance=±5% resistance=220 package=THT]
  Componente1 = Arduino Mega 2560 (Rev3)

nets:
  N1: U1.connector0, Componente1.D12_PWM
  N2: U1.connector1, Componente1.D11_PWM
  N3: U1.connector2, Componente1.D10_PWM
  N4: U1.connector3, Componente1.D9_PWM
  N5: U1.connector4, Componente1.D8_PWM
  N6: U1.connector5, U1.connector7, S1.Pin_3, S1.Pin_4, R1.pin_1, Componente1.5V
  N7: U1.connector8, R2.Pin_0, R3.Pin_1, Componente1.GND
  N8: S1.Pin_1, S1.Pin_2, R3.Pin_0, Componente1.D3_PWM
  N9: R1.pin_0, R2.Pin_1, Componente1.D2_PWM
