# Fritzing sketch id4089_TeslaCoil_schema_0 (saved by Fritzing 0.9.3b)
breadboards: 1

parts:
  Q1 = NPN-Transistor [package="TO92 [THT]"]
  L = Inductor [package="400 mil [THT]"]
  R1 = Resistor [tolerance=±5% resistance=22k package=THT]
  S1 = Toggle Switch [package=THT]
  L_2 = Inductor [package="1206 [SMD]"]
  part = Battery block 9V

nets:
  N1: Q1.E, part.-
  N2: Q1.B, R1.Pin_1, L_2.pin_0
  N3: Q1.C, L.pin_1
  N4: L.pin_0, R1.Pin_0, S1.L2
  N5: S1.COM, part.+
