# Fritzing sketch id408_Arduino_Based_IR_Receiver_for_PC_Remote_0 (saved by Fritzing 0.9.2b)

parts:
  Part1 = Arduino Uno (Rev3)
  LED1 = LED - 5mm [color="Red (633nm)" package="5 mm [THT]"]
  R1 = Resistor [tolerance=±5% resistance=220 package=THT]
  TSOP_1738 = TSOP312.., 314.. [part_number="TSOP 1738" package=THT]

nets:
  N1: Part1.D12/MISO, TSOP_1738.Data
  N2: Part1.D13/SCK, LED1.anode, R1.Pin_0
  GND: Part1.GND, LED1.cathode, TSOP_1738.GND
  N3: Part1.5V, TSOP_1738.Vs
