# Fritzing sketch id4091_photo_inter_0 (saved by Fritzing 0.9.3b)
breadboards: 1

parts:
  Composant1 = Arduino Uno (Rev3)
  U1 = F17
  R1 = Resistor [tolerance=±5% resistance=10k package="0805 [SMD]"]

nets:
  N1: Composant1.A0, U1.connector3, R1.Pin_0
  N2: Composant1.5V, U1.connector0, U1.connector2, R1.Pin_1
  N3: Composant1.GND, U1.connector1
