# Fritzing sketch id4093_IC2ARDUINOEPI_0 (saved by Fritzing 0.9.2b)
breadboards: 1

parts:
  Part1 = Arduino Uno (Rev3)
  Raspberry_Pi1 = Raspberry Pi 2
  DHT2 = DHT11_Temperature_and_Humitidy_Sensor
  R5 = Resistor [tolerance=±5% resistance=220 package=THT]

nets:
  N1: Part1.A4/SDA, Raspberry_Pi1.3v3, Raspberry_Pi1.GPIO2
  N2: Part1.A5/SCL, Raspberry_Pi1.GPIO3
  N3: Part1.D4, DHT2.connector2, R5.Pin_0
  N4: Part1.5V, DHT2.connector1, R5.Pin_1
  GND: Part1.GND, Raspberry_Pi1.GPIO4, Raspberry_Pi1.GND, DHT2.connector4
