# Fritzing sketch id4094_daniel_0 (saved by Fritzing 0.9.3b)
breadboards: 1

parts:
  Bauteil1 = Arduino Uno (Rev3)
  Q1 = NPN-Transistor [package="TO92 [THT]"]
  R1 = Resistor [tolerance=±5% resistance=1k package=THT]
  R2 = Resistor [tolerance=±5% resistance=10k package=THT]
  M1 = DC Motor
  R3 = Rotary Potentiometer (Small) [maximum_resistance=100kΩ package=THT]

nets:
  N1: Bauteil1.A0, R3.wiper
  N2: Bauteil1.D11_PWM/MOSI, R1.Pin_0, R2.Pin_0
  N3: Bauteil1.5V, M1.pin_1, R3.leg1
  N4: Bauteil1.GND, Q1.C, R2.Pin_1, R3.leg2
  N5: Q1.E, M1.pin_2
  N6: Q1.B, R1.Pin_1
