# Fritzing sketch id4095_Conductivity_Test_0 (saved by Fritzing 0.8.5b)
breadboards: 1

parts:
  LED1 = LED - 5mm [color="Red (633nm)" package="5 mm [THT]"]
  R1 = Resistor [tolerance=±5% resistance=220 package=THT]
  Q1 = NPN-Transistor [package="TO92 [THT]"]
  R2 = Resistor [tolerance=±5% resistance=220 package=THT]

nets:
  N1: LED1.cathode, Q1.C
  N2: LED1.anode, R1.Pin_0
  N3: Q1.B, R2.Pin_1
