# Fritzing sketch id4096_To_Jiang_0 (saved by Fritzing 0.9.3b)
breadboards: 1

parts:
  J1 = Screw terminal - 2 pins [package=THT]
  R1 = Resistor [tolerance=±1% resistance=4.7k package="0402 [SMD]"]
  Indicator_L = Optocoupler [package=THT]
  D1 = Rectifier Diode [package="Melf DO-213 AA [SMD]"]
  D2 = Rectifier Diode [package="Melf DO-213 AA [SMD]"]
  Part1 = Arduino Nano (Rev3.0)
  J2 = Screw terminal - 2 pins [package=THT]
  12V_OUT = DC-DC_CONVERTER [package=dc-dc_converter]
  5V_OUT = DC-DC_CONVERTER [package=dc-dc_converter]
  R2 = Resistor [tolerance=±1% resistance=4.7k package="0402 [SMD]"]
  J3 = Screw terminal - 2 pins [package=THT]
  R3 = Resistor [tolerance=±1% resistance=4.7k package="0402 [SMD]"]
  R4 = Resistor [tolerance=±1% resistance=4.7k package="0402 [SMD]"]
  Indicator_R = Optocoupler [package=THT]
  D3 = Rectifier Diode [package="Melf DO-213 AA [SMD]"]
  D4 = Rectifier Diode [package="Melf DO-213 AA [SMD]"]
  J4 = Screw terminal - 2 pins [package=THT]
  R5 = Resistor [tolerance=±1% resistance=4.7k package="0402 [SMD]"]
  R6 = Resistor [tolerance=±1% resistance=4.7k package="0402 [SMD]"]
  Low_Beam = Optocoupler [package=THT]
  D5 = Rectifier Diode [package="Melf DO-213 AA [SMD]"]
  D6 = Rectifier Diode [package="Melf DO-213 AA [SMD]"]
  R7 = Resistor [tolerance=±1% resistance=150 package="0402 [SMD]"]
  Q1 = MOSFET-NCHANNEL [package=to220v]
  LED1 = LED_RING [package=led_ring]

nets:
  GND1: J1.pin1, D2.cathode, 12V_OUT.GND1, 5V_OUT.GND1, D3.cathode, D5.cathode
  VIN: J1.pin2, 12V_OUT.VIN, 5V_OUT.VIN
  N1: R1.Pin_0, J2.pin2
  N2: R1.Pin_1, Indicator_L.Pin_1, D1.cathode
  N3: Indicator_L.Pin_2, D2.anode
  GND2: Indicator_L.Pin_4, Part1.GND, 12V_OUT.GND2, 5V_OUT.GND2, Indicator_R.Pin_4, Low_Beam.Pin_4, Q1.S
  N4: Indicator_L.Pin_5, Part1.A0, R2.Pin_0
  N5: Part1.D11/MOSI, R7.Pin_0
  N6: Part1.VIN, 5V_OUT.VOUT, R2.Pin_1, R4.Pin_1, R6.Pin_1
  N7: Part1.A2, R6.Pin_0, Low_Beam.Pin_5
  N8: Part1.A1, R4.Pin_0, Indicator_R.Pin_5
  N9: 12V_OUT.VOUT, LED1.COM0
  N10: J3.pin2, R3.Pin_0
  N11: R3.Pin_1, Indicator_R.Pin_1, D4.cathode
  N12: Indicator_R.Pin_2, D3.anode, D4.anode
  N13: J4.pin2, R5.Pin_0
  N14: R5.Pin_1, Low_Beam.Pin_1, D6.cathode
  N15: Low_Beam.Pin_2, D5.anode, D6.anode
  N16: R7.Pin_1, Q1.G
  N17: Q1.D, LED1.COM3
