# Fritzing sketch id4099_Nachtlicht_regelbar_0 (saved by Fritzing 0.9.1b)
circuit board: 6.88566cm x 5.36311cm
breadboards: 2

parts:
  R1 = Resistor [tolerance=±5% resistance=220 package=THT]
  R2 = Resistor [tolerance=±5% resistance=220 package=THT]
  R3 = Resistor [tolerance=±5% resistance=220 package=THT]
  LED2 = RGB LED (com. cathode, rbg) [package="5 mm [THT]"]
  R4 = Rotary Potentiometer (Small) [maximum_resistance=100kΩ package=THT]
  Bauteil1 = Arduino Uno (Rev3)

nets:
  N1: R1.Pin_0, Bauteil1.D11_PWM/MOSI
  N2: R1.Pin_1, LED2.red_anode
  N3: R2.Pin_0, Bauteil1.D10_PWM/SS
  N4: R2.Pin_1, LED2.blue_anode
  N5: R3.Pin_0, Bauteil1.D9_PWM
  N6: R3.Pin_1, LED2.green_anode
  N7: LED2.common_cathode, R4.leg1, Bauteil1.GND
  N8: R4.wiper, Bauteil1.A0
  N9: R4.leg2, Bauteil1.5V

notes:
  NACHTLICHT
  Ergänzung zu Beispielprojekt Nachtlicht.
  a- per Poti regelbare Farb-Wechsel
  a-1- Ausgabe der Potistellung in Serial Monitor
