# Fritzing sketch id409_Arduino_Music_Player_circuit_0 (saved by Fritzing 0.9.3b)
breadboards: 1

parts:
  Part1 = Arduino Uno (Rev3)
  Part2 = MicroSD Card Module
  U1 = LM386 [package=dip08]
  S1 = Pushbutton [package="[THT]"]
  S2 = Pushbutton [package="[THT]"]
  C1 = Capacitor Polarized [package=cpol-radial-10uf-25v]
  R1 = Resistor [tolerance=±5% resistance=1k package="2512 [SMD]"]
  C2 = Capacitor Polarized [package=cpol-radial-10uf-25v]
  C3 = Capacitor Polarized [package=panasonic_c]
  R2 = Resistor [tolerance=±5% resistance=10k package="2512 [SMD]"]
  C4 = Capacitor Polarized [package=panasonic_c]
  SP1 = SPEAKER [package=pcb_mount_speaker]

nets:
  N1: Part1.D9_PWM, R1.Pin_0
  N2: Part1.D11_PWM/MOSI, Part2.MOSI
  N3: Part1.D12/MISO, Part2.MISO
  N4: Part1.D13/SCK, Part2.SCK
  N5: Part1.D2, S1.Pin_3, S1.Pin_4
  N6: Part1.D3_PWM, S2.Pin_1, S2.Pin_2
  N7: Part1.D4, Part2.CS
  N8: Part1.5V, U1.V+, C3.+
  N9: Part1.GND, U1.-IN, U1.V-, S1.Pin_1, S1.Pin_2, S2.Pin_3, S2.Pin_4, C2.-, C3.-, SP1.+
  N10: U1.GAIN, C1.+, C1.-
  N11: U1.+IN, R1.Pin_1
  N12: U1.OUT, R2.Pin_0, C4.+
  N13: C2.+, R2.Pin_1
  N14: C4.-, SP1.-
