# Fritzing sketch id40_ShiftR_16FET_0 (saved by Fritzing 0.8.7b)
circuit board: 8.37776cm x 7.16472cm
breadboards: 1

parts:
  U1 = 74HC595 [package="DIP16 [THT]"]
  Input = screw terminal, 5 pins
  Q0 = Basic FET N-Channel [package="TO220 [THT]"]
  Power = Screw terminal - 2 pins [package=THT]
  Q1 = Basic FET N-Channel [package="TO220 [THT]"]
  CH1 = Screw terminal - 2 pins [package=THT]
  Q2 = Basic FET N-Channel [package="TO220 [THT]"]
  CH2 = Screw terminal - 2 pins [package=THT]
  Q3 = Basic FET N-Channel [package="TO220 [THT]"]
  CH3 = Screw terminal - 2 pins [package=THT]
  Q5 = Basic FET N-Channel [package="TO220 [THT]"]
  Q4 = Basic FET N-Channel [package="TO220 [THT]"]
  CH5 = Screw terminal - 2 pins [package=THT]
  CH4 = Screw terminal - 2 pins [package=THT]
  Q7 = Basic FET N-Channel [package="TO220 [THT]"]
  Q6 = Basic FET N-Channel [package="TO220 [THT]"]
  CH7 = Screw terminal - 2 pins [package=THT]
  CH6 = Screw terminal - 2 pins [package=THT]
  U2 = 74HC595 [package="DIP16 [THT]"]
  Q11 = Basic FET N-Channel [package="TO220 [THT]"]
  Q15 = Basic FET N-Channel [package="TO220 [THT]"]
  Q9 = Basic FET N-Channel [package="TO220 [THT]"]
  Q14 = Basic FET N-Channel [package="TO220 [THT]"]
  Q10 = Basic FET N-Channel [package="TO220 [THT]"]
  Q13 = Basic FET N-Channel [package="TO220 [THT]"]
  Q8 = Basic FET N-Channel [package="TO220 [THT]"]
  Q12 = Basic FET N-Channel [package="TO220 [THT]"]
  CH12 = Screw terminal - 2 pins [package=THT]
  CH9 = Screw terminal - 2 pins [package=THT]
  CH8 = Screw terminal - 2 pins [package=THT]
  CH13 = Screw terminal - 2 pins [package=THT]
  CH15 = Screw terminal - 2 pins [package=THT]
  CH11 = Screw terminal - 2 pins [package=THT]
  CH10 = Screw terminal - 2 pins [package=THT]
  CH14 = Screw terminal - 2 pins [package=THT]
  C1 = Capacitor [package=cap-pth-small2]
  Output = screw terminal, 5 pins
  CH0 = Screw terminal - 2 pins [package=THT]
  D1 = Rectifier Diode [part_number=1N4004 package="300 mil [THT]"]

nets:
  N1: U1.Q1, Q1.gate
  N2: U1.Q2, Q2.gate
  N3: U1.Q3, Q3.gate
  N4: U1.Q4, Q4.gate
  N5: U1.Q5, Q5.gate
  N6: U1.Q6, Q6.gate
  N7: U1.Q7, Q7.gate
  GND: U1.GND, U1.OE, Input.pin2, Q0.source, Power.pin1, Q1.source, Q2.source, Q3.source, Q5.source, Q4.source, Q7.source, Q6.source, U2.GND, U2.OE, Q11.source, Q15.source, Q9.source, Q14.source, Q10.source, Q13.source, Q8.source, Q12.source, C1.2, Output.pin2, D1.anode
  N8: U1.Q7', U2.DS
  VCC: U1.MR, U1.VCC, Input.pin1, U2.MR, U2.VCC, Output.pin1
  N9: U1.SH_CP, Input.pin5, U2.SH_CP, Output.pin5
  N10: U1.ST_CP, Input.pin4, U2.ST_CP, C1.1, Output.pin4
  N11: U1.DS, Input.pin3
  N12: U1.Q0, Q0.gate
  N13: Q0.drain, CH0.pin1
  N14: Power.pin2, CH1.pin2, CH2.pin2, CH3.pin2, CH5.pin2, CH4.pin2, CH7.pin2, CH6.pin2, CH12.pin2, CH9.pin2, CH8.pin2, CH13.pin2, CH15.pin2, CH11.pin2, CH10.pin2, CH14.pin2, CH0.pin2, D1.cathode
  N15: Q1.drain, CH1.pin1
  N16: Q2.drain, CH2.pin1
  N17: Q3.drain, CH3.pin1
  N18: Q5.drain, CH5.pin1
  N19: Q4.drain, CH4.pin1
  N20: Q7.drain, CH7.pin1
  N21: Q6.drain, CH6.pin1
  N22: U2.Q1, Q9.gate
  N23: U2.Q2, Q10.gate
  N24: U2.Q3, Q11.gate
  N25: U2.Q4, Q12.gate
  N26: U2.Q5, Q13.gate
  N27: U2.Q6, Q14.gate
  N28: U2.Q7, Q15.gate
  N29: U2.Q7', Output.pin3
  N30: U2.Q0, Q8.gate
  N31: Q11.drain, CH11.pin1
  N32: Q15.drain, CH15.pin1
  N33: Q9.drain, CH9.pin1
  N34: Q14.drain, CH14.pin1
  N35: Q10.drain, CH10.pin1
  N36: Q13.drain, CH13.pin1
  N37: Q8.drain, CH8.pin1
  N38: Q12.drain, CH12.pin1

notes:
  +-
  SH ST DS - +
  Output
