# Fritzing sketch id4101_Test_0 (saved by Fritzing 0.7.0b)
breadboards: 1

parts:
  Nano1 = Arduino Nano v2.3
  LED1 = LED - 3mm [color="Red (633nm)" package="3 mm [THT]"]

nets:
  N1: Nano1.GND, LED1.cathode
  N2: Nano1.D13, LED1.anode
