# Fritzing sketch id4102_Test_Transistor_0 (saved by Fritzing 0.8.7b)
circuit board: 8.46667cm x 5.64444cm
breadboards: 1

parts:
  Q3 = Basic FET N-Channel [package="TO220 [THT]"]
  BAT1 = BC9VPC [package=bc9vpc]
  Q4 = Basic FET N-Channel [package="TO220 [THT]"]
  Q5 = Basic FET N-Channel [package="TO220 [THT]"]
  Part1 = Arduino Uno (Rev3)
  LED1 = LED - 3mm [color="Red (633nm)" package="3 mm [THT]"]
  R1 = Resistor [tolerance=±5% resistance=220 package=THT]
  R2 = Resistor [tolerance=±5% resistance=220 package=THT]
  R3 = Resistor [tolerance=±5% resistance=220 package=THT]
  LED2 = LED - 3mm [color="Red (633nm)" package="3 mm [THT]"]
  LED3 = LED - 3mm [color="Red (633nm)" package="3 mm [THT]"]

nets:
  N1: Q3.gate, Part1.D9_PWM
  GND: Q3.drain, BAT1.V+, BAT1.V-, Q4.drain, Q5.drain, Part1.GND, Part1.VIN, R1.Pin_1, R2.Pin_1, R3.Pin_1
  N2: Q3.source, LED1.anode
  N3: Q4.gate, Part1.D10_PWM/SS
  N4: Q4.source, LED2.anode
  N5: Q5.gate, Part1.D11_PWM/MOSI
  N6: Q5.source, LED3.anode
  N7: LED1.cathode, R1.Pin_0
  N8: R2.Pin_0, LED2.cathode
  N9: R3.Pin_0, LED3.cathode
