# Fritzing sketch id4104_Untitled_Sketch_0 (saved by Fritzing 0.9.3b)
circuit board: 8.46667cm x 5.64444cm
breadboards: 1

parts:
  Part1 = Arduino Uno (Rev3)
  R1 = Resistor [tolerance=±5% resistance=10k package=THT]
  R2 = Resistor [tolerance=±5% resistance=10k package=THT]
  R3 = Resistor [tolerance=±5% resistance=10k package=THT]
  R4 = Resistor [tolerance=±5% resistance=10k package=THT]
  R5 = Resistor [tolerance=±5% resistance=10k package=THT]
  R6 = Resistor [tolerance=±5% resistance=10k package=THT]
  R7 = Resistor [tolerance=±5% resistance=10k package=THT]
  J1 = shrouded pin header, 8 pins [form="♂ (shrouded male)"]

nets:
  N1: Part1.D8, R1.Pin_1, J1.pin8
  N2: Part1.GND, R1.Pin_0, R2.Pin_0, R3.Pin_0, R4.Pin_0, R5.Pin_0, R6.Pin_0, R7.Pin_0
  N3: Part1.D1/TX, R7.Pin_1, J1.pin1
  N4: Part1.D2, R6.Pin_1, J1.pin2
  N5: Part1.D3_PWM, R5.Pin_1, J1.pin3
  N6: Part1.D4, R4.Pin_1, J1.pin4
  N7: Part1.D6_PWM, R3.Pin_1, J1.pin6
  N8: Part1.D7, R2.Pin_1, J1.pin7
  N9: Part1.5V, J1.pin5
