# Fritzing sketch id4105_arduino_camera_shutter_0 (saved by Fritzing 0.9.0b)
breadboards: 1

parts:
  元件1 = Arduino Uno (Rev3)
  U1 = Optocoupler [package=THT]
  U2 = Optocoupler [package=THT]
  R1 = Resistor [tolerance=±10% resistance=220 package=THT]
  LED1 = LED - 3mm [color="Red (633nm)" package="3 mm [THT]"]
  LED2 = LED - 3mm [color="Red (633nm)" package="3 mm [THT]"]  # not connected
  R2 = Resistor [tolerance=±10% resistance=220 package=THT]  # not connected

nets:
  N1: 元件1.D4, LED1.anode
  N2: 元件1.GND, U1.Pin_2
  N3: U1.Pin_1, R1.Pin_0
  N4: U1.Pin_3, U2.Pin_3
  N5: R1.Pin_1, LED1.cathode

notes:
  Focus CG Shutter
