# Fritzing sketch id4106_test1_0 (saved by Fritzing 0.9.3b)
breadboards: 2

parts:
  パーツ1 = Arduino Uno (Rev3)
  U1 = 74HC595 [package="DIP16 [THT]"]
  C2 = Ceramic Capacitor [capacitance=100nF package="100 mil [THT, multilayer]"]
  LED1 = LED - 5mm [color="Red (633nm)" package="5 mm [THT]"]
  R1 = Resistor [tolerance=±5% resistance=220 package=THT]
  LED2 = LED - 5mm [color="Red (633nm)" package="5 mm [THT]"]
  R2 = Resistor [tolerance=±5% resistance=220 package=THT]
  LED3 = LED - 5mm [color="Red (633nm)" package="5 mm [THT]"]
  R3 = Resistor [tolerance=±5% resistance=220 package=THT]
  LED4 = LED - 5mm [color="Red (633nm)" package="5 mm [THT]"]
  R4 = Resistor [tolerance=±5% resistance=220 package=THT]
  LED5 = LED - 5mm [color="Red (633nm)" package="5 mm [THT]"]
  R5 = Resistor [tolerance=±5% resistance=220 package=THT]
  LED6 = LED - 5mm [color="Red (633nm)" package="5 mm [THT]"]
  R6 = Resistor [tolerance=±5% resistance=220 package=THT]
  LED7 = LED - 5mm [color="Red (633nm)" package="5 mm [THT]"]
  R7 = Resistor [tolerance=±5% resistance=220 package=THT]
  LED8 = LED - 5mm [color="Red (633nm)" package="5 mm [THT]"]
  R8 = Resistor [tolerance=±5% resistance=220 package=THT]

nets:
  N1: パーツ1.D8, U1.ST_CP, C2.0
  N2: パーツ1.D11_PWM/MOSI, U1.DS
  N3: パーツ1.D12/MISO, U1.SH_CP
  5V: パーツ1.5V, U1.MR, U1.VCC
  GND: パーツ1.GND, U1.GND, U1.OE, C2.1, LED1.cathode, LED2.cathode, LED3.cathode, LED4.cathode, LED5.cathode, LED6.cathode, LED7.cathode, LED8.cathode
  N4: U1.Q1, R2.Pin_1
  N5: U1.Q2, R3.Pin_1
  N6: U1.Q3, R4.Pin_1
  N7: U1.Q4, R5.Pin_1
  N8: U1.Q5, R6.Pin_1
  N9: U1.Q6, R7.Pin_1
  N10: U1.Q7, R8.Pin_1
  N11: U1.Q0, R1.Pin_1
  N12: LED1.anode, R1.Pin_0
  N13: LED2.anode, R2.Pin_0
  N14: LED3.anode, R3.Pin_0
  N15: LED4.anode, R4.Pin_0
  N16: LED5.anode, R5.Pin_0
  N17: LED6.anode, R6.Pin_0
  N18: LED7.anode, R7.Pin_0
  N19: LED8.anode, R8.Pin_0
