# Fritzing sketch id4109_Untitled_Sketch_2_0 (saved by Fritzing 0.9.3b)
breadboards: 1

parts:
  元件2 = Arduino Nano (Rev3.0) (ICSP)
  S1 = Pushbutton [package="[THT]"]
  S2 = Momentary Switch [package=ksa_sealed_tac_switch]
  元件3 = LED Matrix - Serial Interface - Red/Green/Blue  # not connected
  元件5 = LED Matrix - Serial Interface - Red/Green/Blue  # not connected
  元件6 = LED Matrix - Serial Interface - Red/Green/Blue  # not connected
  元件7 = LED Matrix - Serial Interface - Red/Green/Blue  # not connected
  元件8 = LED Matrix - Serial Interface - Red/Green/Blue  # not connected
  RHT1 = Humidity and Temperature Sensor RHT03
  R1 = PHOTOCELL [package=photocell-kit]
  元件4 = LED Matrix - Serial Interface - Red/Green/Blue
  R2 = Resistor [tolerance=±5% resistance=220 package="2010 [SMD]"]
  S3 = SWITCH-DPDT [package=ms]
  J1 = Basic Servo
  J2 = Basic Servo
  hc-sr1 = hc-sr04
  LED1 = LEDs [package=fkit-led-1206]
  LED2 = LEDs [package=fkit-led-1206]
  LED3 = LEDs [package=fkit-led-1206]
  S4 = Round Pushbutton
  S5 = Reed switch [package=THT]
  R3 = Resistor [tolerance=±5% resistance=220 package="1206 [SMD]"]

nets:
  GND: 元件2.GND, S1.Pin_1, S1.Pin_2, S2.2, RHT1.GND_2, R2.Pin_0, S3.5, J1.gnd, J2.gnd, hc-sr1.GND, LED3.A, S4.leg0, R3.Pin_1
  N1: 元件2.D2, S1.Pin_4
  N2: 元件2.D3, S2.4
  N3: 元件2.D4, 元件4.SCK
  N4: 元件2.D5, hc-sr1.Trig
  N5: 元件2.D6, LED1.C
  N6: 元件2.D7, hc-sr1.Echo
  N7: 元件2.D8, RHT1.Data-signal
  N8: 元件2.D9, J2.pulse
  N9: 元件2.D10, S4.leg1
  N10: 元件2.D11/MOSI, 元件4.GND
  N11: 元件2.D12/MISO, S3.6
  VCC: 元件2.5V, RHT1.Vcc, R1.P$1, J1.vcc, J2.vcc, hc-sr1.VCC, S5.pin_2
  N12: 元件2.A3, 元件4.CS
  N13: 元件2.A2, 元件4.MISO
  N14: 元件2.A1, S5.pin_1, R3.Pin_0
  N15: 元件2.A0, R1.P$2, R2.Pin_1
  N16: 元件2.D13/SCK, J1.pulse
  N17: LED1.A, LED2.C
  N18: LED2.A, LED3.C

notes:
  right turing button
  left turing button
  [LED matrix]
  DATA 16 (A2)
  WR 17 (A3)
  CS 4
  CS2(RD) 11<module fritzingVersion="0.9.3b.04.19.5c895d327c44a3114e5fcc9d8260daf0cbb52806">
  <boundingRects>
  <boundingRect name="概要圖檢視" rect="0 0 0 0"/>
  <boundingRect name="麵包板檢視" rect="225.165 369.754 80.6667 88"/>
  <boundingRect name="PCB 檢視" rect="0 0 0 0"/>
  </boundingRects>
  <instances>
  <instance moduleIdRef="NoteModuleID" modelIndex="6718" path=":/resources/parts/core/note.fzp">
  <title>Note2</title>
  <text>&lt;!DOCTYPE HTML PUBLIC "-//W3C//DTD HTML 4.0//EN" "http://www.w3.org/TR/REC-html40/strict.dtd">
  &lt;html>&lt;head>&lt;meta name="qrichtext" content="1" />&lt;style type="text/css">
  p, li { white-space: pre-wrap; }
  &lt;/style>&lt;/head>&lt;body style=" font-family:'Droid Sans'; font-size:9pt; font-weight:400; font-style:normal;">
  &lt;p style=" margin-top:0px; margin-bottom:0px; margin-left:0px; margin-right:0px; -qt-block-indent:0; text-indent:0px;">[LED matrix]&lt;br />&lt;/p>
  &lt;p style=" margin-top:0px; margin-bottom:0px; margin-left:0px; margin-right:0px; -qt-block-indent:0; text-indent:0px;">DATA 16 (A2)&lt;/p>
  &lt;p style=" margin-top:0px; margin-bottom:0px; margin-left:0px; margin-right:0px; -qt-block-indent:0; text-indent:0px;">WR 17 (A3)&lt;/p>
  &lt;p style=" margin-top:0px; margin-bottom:0px; margin-left:0px; margin-right:0px; -qt-block-indent:0; text-indent:0px;">CS 4&lt;/p>
  &lt;p style=" margin-top:0px; margin-bottom:0px; margin-left:0px; margin-right:0px; -qt-block-indent:0; text-indent:0px;">CS2(RD) 11&lt;/p>&lt;/body>&lt;/html></text>
  <views>
  <breadboardView layer="breadboardNote">
  <geometry width="80.6667" height="88" x="225.165" y="369.754" z="6.50001"/>
  </breadboardView>
  </views>
  </instance>
  </instances>
  </module>
  [DHT11]
  Vcc 5V
  Data 8
  No no
  Gnd gnd
  [Photoresist]
  [Toggle switch]
  servo moter (open box)
  servo moter (hand)
  back
  middle
  front
  [SMD LED]
