# Fritzing sketch id410_Arduino_OBD_k_Line_SubaruClockPod_0 (saved by Fritzing 0.9.3b)
breadboards: 1

parts:
  Part1 = Arduino Uno (Rev3)
  U1 = OP482 - Low Power, High Speed JFET Quad Operational Amplifier [part_number=LM339]
  J1 = shrouded pin header, 10 pins [form="♂ (shrouded male)"]
  R2 = Resistor [tolerance=±5% resistance=10k package=THT]
  R1 = Resistor [tolerance=±5% resistance=10k package=THT]
  VCC1 = Battery block 9V
  R3 = Resistor [tolerance=±5% resistance=10k package=THT]
  R4 = Resistor [tolerance=±5% resistance=10k package=THT]
  R5 = Resistor [tolerance=±5% resistance=10k package=THT]
  R6 = Resistor [tolerance=±5% resistance=10k package=THT]

nets:
  N1: Part1.D10_PWM/SS, U1.OUTA, R1.Pin_1
  N2: Part1.D11_PWM/MOSI, U1.+INB
  N3: Part1.5V, R1.Pin_0, R6.Pin_1
  N4: Part1.GND, U1.+IND, J1.pin1, VCC1.-, R3.Pin_0, R5.Pin_0
  N5: U1.-INA, U1.OUTB, J1.pin8, R2.Pin_1
  N6: U1.+INA, J1.pin5, R2.Pin_0, VCC1.+, R4.Pin_1
  N7: U1.V+, R5.Pin_1, R6.Pin_0
  N8: U1.-INB, R3.Pin_1, R4.Pin_0

notes:
  This is the LM339, not the OP482
  This is a stand-in for a DB-9 that leads to the OBD port.
  Pin labels from left to right, top to bottom:
  1
  2
  3: K-line
  4
  5
  6: Gnd
  7
  8
  9
  10: 12V
  These assignments are arbitrary, so change them if you have other pin orders needed
  This represents the car's power supply (either the 12V from the OBD port, or 12V from some other source)
  The three connected pins are:
  3: K-line
  6: 12V
  10: Ground
  Again, this is the LM339, not the OP482
  Thus, the connected pins are:
  OP482 vs LM339
  OUTA = OUT1
  -INA = OUT2
  +INA = V+
  V+ = 2IN-
  +INB = 2IN+
  -INB = 1IN-
  OUTB = 1IN+
  +IND = Gnd
  10 is Rx
  11 is Tx
