# Fritzing sketch id4111_schaltung_0 (saved by Fritzing 0.9.3b)

parts:
  Bauteil2 = Arduino Nano (Rev3.0)
  Servo_Hinten = Basic Servo
  Servo_Mitte = Basic Servo
  Servo_Vorne = Basic Servo
  Sensor_Links = fc-51 [package=THT]
  Sensor_Rechts = fc-51 [package=THT]
  Wiederstand_10k = Resistor [tolerance=±5% resistance=220 package=THT]
  9V_Batterie = BC9VPC [package=bc9vpc]
  S3 = Pushbutton [package="[THT]"]
  Schalter = SPST Switch [package=switch-spdt-smd]

nets:
  GND: Bauteil2.GND, Servo_Hinten.gnd, Servo_Mitte.gnd, Servo_Vorne.gnd, Sensor_Links.pin2, Sensor_Rechts.pin2, Wiederstand_10k.Pin_0, Schalter.O
  N1: Bauteil2.D2, Sensor_Links.pin1
  N2: Bauteil2.D4, Sensor_Rechts.pin1
  N3: Bauteil2.D9, Servo_Hinten.pulse
  N4: Bauteil2.D10, Servo_Vorne.pulse
  N5: Bauteil2.D11/MOSI, Servo_Mitte.pulse
  N6: Bauteil2.D12/MISO, S3.Pin_3, S3.Pin_4
  N7: Bauteil2.VIN, 9V_Batterie.V+
  VCC: Bauteil2.5V, Servo_Hinten.vcc, Servo_Mitte.vcc, Servo_Vorne.vcc, Sensor_Links.pin3, Sensor_Rechts.pin3, Wiederstand_10k.Pin_1, S3.Pin_1, S3.Pin_2
  N8: 9V_Batterie.V-, Schalter.P
