# Fritzing sketch id4113_Servo_Tester_0 (saved by Fritzing 0.8.7b)
breadboards: 1

parts:
  IC1 = General purpose bipolar Timer [package=dil-08]
  R1 = Rotary Potentiometer (Large) [maximum_resistance=100kΩ package=THT]
  R2 = Resistor [tolerance=±5% resistance=680k package=THT]
  R3 = Resistor [tolerance=±5% resistance=18k package=THT]
  C2 = Ceramic Capacitor [capacitance=100nF package="100 mil [THT, multilayer]"]
  C3 = Tantalum Capacitor [capacitance=10pF package="100 mil [THT, tantalum]"]
  D1 = Diode [package=diode-1n4148]

nets:
  N1: IC1.GND, C2.0, C3.+
  N2: IC1.TRI, IC1.TRE, R2.Pin_0, C2.1, D1.A
  N3: IC1._RES, IC1.VCC+, R3.Pin_0
  N4: IC1.CON, C3.-
  N5: IC1.DIS, R1.wiper
  N6: R1.leg1, R2.Pin_1
  N7: R1.leg2, R3.Pin_1

notes:
  Testador de Servo Motor
  E
  Acionador ESC
  Preto > GND
  Branco > Sinal
  Vermelho > +5v
  Ligar direto no ESC
  Materiais:
  1 diodo 1n4148
  1 resistor 18k
  1 resistor 680k
  1 capacitor 0.1uf (104)
  1 capacitor 0.033uf (333)
  1 Circuito Integrado NE555
  1 Potenciometro 50k
