# Fritzing sketch id4114_shift (saved by Fritzing 0.3.16b)
breadboards: 1

parts:
  595 = 74HC595 [package="DIP16 [THT]"]
  J1 = female pin header, 2 pins [form="♀ (female)"]
  J2 = female pin header, 2 pins [form="♀ (female)"]
  C1 = female pin header, 2 pins [form="♀ (female)"]
  DIn = female pin header, 3 pins [form="♀ (female)"]
  DOut = female pin header, 3 pins [form="♀ (female)"]
  I/O = female pin header, 8 pins [form="♀ (female)"]
  DC_Power1 = DC Power [voltage=5]

nets:
  N1: 595.Q1, I/O.pin2
  N2: 595.Q2, I/O.pin3
  N3: 595.Q3, I/O.pin4
  N4: 595.Q4, I/O.pin5
  N5: 595.Q5, I/O.pin6
  N6: 595.Q6, I/O.pin7
  N7: 595.Q7, I/O.pin8
  GND: 595.GND, 595.OE, J1.pin1, J2.pin1, C1.pin2, DC_Power1.GND
  N8: 595.Q7', DOut.pin3
  N9: 595.MR, 595.VCC, J1.pin2, J2.pin2, DC_Power1.V+
  N10: 595.SH_CP, DIn.pin3, DOut.pin1
  N11: 595.ST_CP, C1.pin1, DIn.pin2, DOut.pin2
  N12: 595.DS, DIn.pin1
  N13: 595.Q0, I/O.pin1

notes:
  serial
  latch
  Out In
  clock
  Power
  - +
