# Fritzing sketch id4116_tester_UTP_with_4017_0 (saved by Fritzing 0.9.3b)
circuit board: 5.5cm x 5.5cm
circuit board: 4.5cm x 5.5cm
stripboards: 2

parts:
  U1 = IC4017-2 [part_number=4017]
  U2 = RJ45 Jack [package=rj45-8]
  R1 = Resistor [tolerance=±5% resistance=1k package=THT]
  R2 = Resistor [tolerance=±5% resistance=1k package=THT]
  R3 = Resistor [tolerance=±5% resistance=1k package=THT]
  R4 = Resistor [tolerance=±5% resistance=1k package=THT]
  R5 = Resistor [tolerance=±5% resistance=1k package=THT]
  R6 = Resistor [tolerance=±5% resistance=1k package=THT]
  R7 = Resistor [tolerance=±5% resistance=1k package=THT]
  R8 = Resistor [tolerance=±5% resistance=1k package=THT]
  R9 = Resistor [tolerance=±5% resistance=1k package=THT]
  LED1 = LED - 3mm [color="Red (633nm)" package="3 mm [THT]"]
  LED2 = LED - 3mm [color="Red (633nm)" package="3 mm [THT]"]
  LED3 = LED - 3mm [color="Red (633nm)" package="3 mm [THT]"]
  LED4 = LED - 3mm [color="Red (633nm)" package="3 mm [THT]"]
  LED5 = LED - 3mm [color="Red (633nm)" package="3 mm [THT]"]
  LED6 = LED - 3mm [color="Red (633nm)" package="3 mm [THT]"]
  LED7 = LED - 3mm [color="Red (633nm)" package="3 mm [THT]"]
  LED8 = LED - 3mm [color="Red (633nm)" package="3 mm [THT]"]
  LED9 = LED - 3mm [color="Green (555nm)" part_number=Blinking package="3 mm [THT]"]
  VCC1 = Battery block 9V
  S1 = Toggle Switch [package=THT]
  U3 = RJ45 Jack [package=rj45-8]
  R10 = Resistor [tolerance=±5% resistance=1k package=THT]
  R11 = Resistor [tolerance=±5% resistance=1k package=THT]
  R12 = Resistor [tolerance=±5% resistance=1k package=THT]
  R13 = Resistor [tolerance=±5% resistance=1k package=THT]
  R14 = Resistor [tolerance=±5% resistance=1k package=THT]
  R15 = Resistor [tolerance=±5% resistance=1k package=THT]
  R16 = Resistor [tolerance=±5% resistance=1k package=THT]
  R17 = Resistor [tolerance=±5% resistance=1k package=THT]
  LED10 = LED - 3mm [color="Red (633nm)" package="3 mm [THT]"]
  LED11 = LED - 3mm [color="Red (633nm)" package="3 mm [THT]"]
  LED12 = LED - 3mm [color="Red (633nm)" package="3 mm [THT]"]
  LED13 = LED - 3mm [color="Red (633nm)" package="3 mm [THT]"]
  LED14 = LED - 3mm [color="Red (633nm)" package="3 mm [THT]"]
  LED15 = LED - 3mm [color="Red (633nm)" package="3 mm [THT]"]
  LED16 = LED - 3mm [color="Red (633nm)" package="3 mm [THT]"]
  LED17 = LED - 3mm [color="Red (633nm)" package="3 mm [THT]"]

nets:
  N1: U1.connector0, R6.Pin_0, LED6.anode
  N2: U1.connector1, R2.Pin_0, LED2.anode
  N3: U1.connector2, R1.Pin_0, LED1.anode
  N4: U1.connector3, R3.Pin_0, LED3.anode
  N5: U1.connector4, R7.Pin_0, LED7.anode
  N6: U1.connector5, R8.Pin_0, LED8.anode
  N7: U1.connector6, R4.Pin_0, LED4.anode
  N8: U1.connector7, R1.Pin_1, R2.Pin_1, R3.Pin_1, R4.Pin_1, R5.Pin_1, R6.Pin_1, R7.Pin_1, R8.Pin_1, S1.L1, S1.COM
  N9: U1.connector9, R5.Pin_0, LED5.anode
  N10: U1.connector10, U1.connector14
  N11: U1.connector12, LED9.cathode
  N12: U1.connector13, R9.Pin_1, LED9.anode
  N13: U1.connector15, R9.Pin_0, VCC1.+
  N14: U2.1, LED1.cathode
  N15: U2.2, LED2.cathode
  N16: U2.3, LED3.cathode
  N17: U2.4, LED4.cathode
  N18: U2.5, LED5.cathode
  N19: U2.6, LED6.cathode
  N20: U2.7, LED7.cathode
  N21: U2.8, LED8.cathode
  N22: VCC1.-, S1.L2
  N23: U3.1, R10.Pin_0, LED10.anode
  N24: U3.2, R11.Pin_0, LED11.anode
  N25: U3.3, R12.Pin_0, LED12.anode
  N26: U3.4, R13.Pin_0, LED13.anode
  N27: U3.5, R14.Pin_0, LED14.anode
  N28: U3.6, R15.Pin_0, LED15.anode
  N29: U3.7, R16.Pin_0, LED16.anode
  N30: U3.8, R17.Pin_0, LED17.anode
  N31: R10.Pin_1, R11.Pin_1, R12.Pin_1, R13.Pin_1, R14.Pin_1, R15.Pin_1, R16.Pin_1, R17.Pin_1, LED10.cathode, LED11.cathode, LED12.cathode, LED13.cathode, LED14.cathode, LED15.cathode, LED16.cathode, LED17.cathode

notes:
  Tester UTP cable, Device for testing network cables. 4017 - Decade counter step by step lights up the LEDs for checking The cable.
  Attention: LED9 must be blinking LED. A LED which has a built-in blinking IC.
  Attention: Green LED must be blinking LED. A LED which has a built-in blinking IC.
  Tester UTP cable
