# Fritzing sketch id4124_TextoAnalogicoConSonido_luz_0 (saved by Fritzing 0.9.2b)
circuit board: 8.46667cm x 5.64444cm
breadboards: 1

parts:
  Onderdeel1 = Arduino Uno (Rev3)
  LCM1602_IIC1 = generic_ic_dip_22_300mil.fzp [part_number="LCM1602 IIC" chip_label="LCM1602 IIC"]
  R2_-_220Ω = Resistor [tolerance=±5% resistance=220 package=THT]
  LCD1 = LCD screen
  R1 = Trimmer Potentiometer [maximum_resistance=10kΩ package=THT]
  LED1 = LED - 5mm [color="Green (570nm)" package="5 mm [THT]"]
  LED2 = LED - 5mm [color="Red (633nm)" package="5 mm [THT]"]
  J1 = Piezo Speaker

nets:
  N1: Onderdeel1.A0, R1.wiper
  N2: Onderdeel1.D9_PWM, R2_-_220Ω.Pin_1
  N3: Onderdeel1.GND, LCM1602_IIC1.connector16, R1.leg2, LED1.cathode, J1.pin1
  N4: Onderdeel1.A4/SDA, LCM1602_IIC1.connector18
  N5: Onderdeel1.A5/SCL, LCM1602_IIC1.connector19
  N6: Onderdeel1.5V, LCM1602_IIC1.connector17, R1.leg1, LED2.anode, J1.pin2
  N7: LCM1602_IIC1.connector0, LCD1.VSS
  N8: LCM1602_IIC1.connector1, LCD1.VDD
  N9: LCM1602_IIC1.connector2, LCD1.V0
  N10: LCM1602_IIC1.connector3, LCD1.RS
  N11: LCM1602_IIC1.connector4, LCD1.R/W
  N12: LCM1602_IIC1.connector5, LCD1.E
  N13: LCM1602_IIC1.connector6, LCD1.DB0
  N14: LCM1602_IIC1.connector7, LCD1.DB1
  N15: LCM1602_IIC1.connector8, LCD1.DB2
  N16: LCM1602_IIC1.connector9, LCD1.DB3
  N17: LCM1602_IIC1.connector10, LCD1.DB4
  N18: LCM1602_IIC1.connector11, LCD1.DB5
  N19: LCM1602_IIC1.connector12, LCD1.DB6
  N20: LCM1602_IIC1.connector13, LCD1.DB7
  N21: LCM1602_IIC1.connector14, LCD1.LED+
  N22: LCM1602_IIC1.connector15, LCD1.LED-
  N23: LCM1602_IIC1.connector20, LCM1602_IIC1.connector21
  N24: R2_-_220Ω.Pin_0, LED1.anode
