# Fritzing sketch id4125_Texto_en_Movimiento_0 (saved by Fritzing 0.9.3b)
breadboards: 1

parts:
  Componente1 = Arduino Uno (Rev3)
  LCD1 = LCD screen

nets:
  N1: Componente1.D9_PWM, LCD1.E
  N2: Componente1.D11_PWM/MOSI, LCD1.RS
  N3: Componente1.D3_PWM, LCD1.DB7
  N4: Componente1.D4, LCD1.DB6
  N5: Componente1.D5_PWM, LCD1.DB5
  N6: Componente1.D6_PWM, LCD1.DB4
  5V: Componente1.5V, LCD1.VDD, LCD1.LED+
  GND: Componente1.GND, LCD1.VSS, LCD1.V0, LCD1.R/W, LCD1.LED-
