# Fritzing sketch id4126_Arduino_0 (saved by Fritzing 0.7.5b)
breadboards: 1

parts:
  LCD1 = LCD screen
  Arduino1 = Arduino
  RE1 = Rotary Encoder [package=THT]

nets:
  VSS: LCD1.VSS, LCD1.R/W, Arduino1.GND, RE1.EncoderPinA
  VDD: LCD1.VDD, Arduino1.+5V, RE1.EncoderPinB
  N1: LCD1.RS, Arduino1.D12
  N2: LCD1.E, Arduino1.D11
  N3: LCD1.DB4, Arduino1.D5
  N4: LCD1.DB5, Arduino1.D4
  N5: LCD1.DB6, Arduino1.D3
