# Fritzing sketch id4128_Texto_en_movimiento_LCD__(1)_KELENY_1_0 (saved by Fritzing 0.7.5b)
breadboards: 1

parts:
  LCD1 = LCD screen
  Arduino1 = Arduino
  R1 = Rotary Potentiometer (Small) [maximum_resistance=100kΩ]

nets:
  N1: LCD1.VSS, LCD1.R/W, LCD1.LED-, R1.leg2
  N2: LCD1.VDD, LCD1.LED+, R1.leg1
  N3: LCD1.V0, R1.wiper
  N4: LCD1.RS, Arduino1.D12
  N5: LCD1.E, Arduino1.D11
