# Fritzing sketch id412_Calculator_0 (saved by Fritzing 0.9.3b)
breadboards: 1

parts:
  Part1 = Arduino Uno (Rev3)
  U1 = LCD-16X2 [package=lcd-16x2]
  U2 = POT [package=pot_mammoth]
  R1 = Resistor [tolerance=±5% resistance=1k package="0603 [SMD]"]
  Matrix_keypad1 = CMG
  S1 = Pushbutton [package="[SMD]"]
  R3 = Resistor [tolerance=±5% resistance=1k package="0603 [SMD]"]
  S5 = Toggle Switch [package=THT]
  VCC1 = Battery block 9V

nets:
  N1: Part1.A0, S1.Pin_1, S1.Pin_2, R3.Pin_0
  N2: Part1.A2, Matrix_keypad1.connector25
  N3: Part1.A3, Matrix_keypad1.connector26
  N4: Part1.A4/SDA, Matrix_keypad1.connector27
  N5: Part1.A5/SCL, Matrix_keypad1.connector28
  N6: Part1.D8, U1.E
  N7: Part1.D9_PWM, U1.DB4
  N8: Part1.D10_PWM/SS, U1.DB5
  N9: Part1.D11_PWM/MOSI, U1.DB6
  N10: Part1.D12/MISO, U1.DB7
  GND: Part1.GND, U1.VSS, U1.R_W, U1.K, U2.S, R1.Pin_1, S1.Pin_3, S1.Pin_4, R3.Pin_1, S5.L1, VCC1.-
  N11: Part1.D2, Matrix_keypad1.connector29
  N12: Part1.D3_PWM, Matrix_keypad1.connector30
  N13: Part1.D4, Matrix_keypad1.connector31
  N14: Part1.D5_PWM, Matrix_keypad1.connector32
  N15: Part1.D7, U1.RS
  5V: Part1.5V, U1.VDD, U2.E, S5.COM
  N16: U1.VO, U2.A
  N17: U1.A, R1.Pin_0
  N18: S5.L2, VCC1.+
