# Fritzing sketch id4130_convert_tft_0 (saved by Fritzing 0.7.7b)
perfboards: 1

parts:
  U1 = Arduino Mega  # not connected
  J1 = double row female pin header, 8 pins [form="♀ (female)"]
  J2 = double row female pin header, 8 pins [form="♀ (female)"]
  J3 = double row female pin header, 8 pins [form="♀ (female)"]
  J4 = double row female pin header, 6 pins [form="♀ (female)"]  # not connected
  J5 = longpad pin header, 18 pins [form="long pad"]
  J6 = longpad pin header, 18 pins [form="long pad"]

nets:
  N1: J1.pin3, J6.pin17
  N2: J1.pin4, J6.pin16
  N3: J1.pin5, J5.pin16
  N4: J1.pin6, J5.pin17
  N5: J1.pin7, J2.pin6, J6.pin2
  N6: J1.pin8, J2.pin5, J5.pin2
  N7: J2.pin1, J5.pin4
  N8: J2.pin2, J3.pin2, J6.pin4
  N9: J2.pin3, J3.pin3, J5.pin3
  N10: J2.pin4, J3.pin1, J6.pin3
  N11: J2.pin7, J5.pin1
  N12: J2.pin8, J6.pin1
  N13: J3.pin4, J6.pin11
  N14: J3.pin5, J5.pin10
  N15: J3.pin6, J6.pin10

notes:
  TFT 2.8 Touchscreen Converter to Arduino MEGA [http://blog.ozzie.web.id/?p=1014]
