# Fritzing sketch id4131_THADLED_0 (saved by Fritzing 0.7.7b)
breadboards: 1

parts:
  Nano1 = Arduino Nano v2.3
  R1 = Resistor [tolerance=±5% resistance=220 package=THT]
  R2 = Resistor [tolerance=±5% resistance=220 package=THT]
  R3 = Resistor [tolerance=±5% resistance=220 package=THT]
  Q1 = Basic FET P-Channel [package="TO220 [THT]"]
  Q2 = Basic FET P-Channel [package="TO220 [THT]"]
  Q3 = Basic FET P-Channel [package="TO220 [THT]"]
  Chase1 = LED - 5mm [color="White (6500K)" package="5 mm [THT]"]
  Chase2 = LED - 5mm [color="White (6500K)" package="5 mm [THT]"]
  Chase3 = LED - 5mm [color="White (6500K)" package="5 mm [THT]"]

nets:
  GND: Nano1.GND, Q1.drain, Q2.drain, Q3.drain
  N1: Nano1.D2, R3.Pin_0
  N2: Nano1.D3, R2.Pin_0
  N3: Nano1.D4, R1.Pin_0
  N4: R1.Pin_1, Q1.gate
  N5: R2.Pin_1, Q2.gate
  N6: R3.Pin_1, Q3.gate
  N7: Q1.source, Chase1.cathode
  N8: Q2.source, Chase2.cathode
  N9: Q3.source, Chase3.cathode
  12V: Chase1.anode, Chase2.anode, Chase3.anode

notes:
  Input from DMX
  To Strip LEDs
