# Fritzing sketch id4132_schematic_0 (saved by Fritzing 0.7.10b)
breadboards: 1

parts:
  Arduino1 = Arduino
  R1 = Rotary Potentiometer (Large) [package=THT]
  J1 = Basic Force Sensing Resistor (FSR) [package=THT]
  R2 = 100k Ω Resistor [package=THT]

nets:
  N1: Arduino1.GND, R1.wiper, J1.pin_1
  N2: Arduino1.+5V, R1.leg1, R2.Pin_0
  N3: Arduino1.A0, R1.leg2
  N4: Arduino1.A1, J1.pin_0, R2.Pin_1
