# Fritzing sketch id4133_atmega32_programandBootload_0 (saved by Fritzing 0.4.3b)
breadboards: 2

parts:
  Arduino1 = Arduino
  LED2 = Red LED - 5mm
  LED1 = Blue LED - 5mm
  LED3 = green LED - 5mm
  R2 = Resistor [resistance=220 package=THT]
  Atmel's_Atmega32L_Microchip1 = AVR-Atmega32
  U1 = Voltage Regulator - 5V [package="TO220 [THT]"]
  VCC1 = Battery block 9V
  XTAL1 = Crystal [package=THT]
  LED4 = green LED - 5mm
  R3 = Resistor [resistance=10k package=THT]
  C3 = Ceramic Disk Capacitor [package=THT]
  C4 = Ceramic Disk Capacitor [package=THT]
  C2 = Electrolytic Capacitor [package=THT]
  C1 = Electrolytic Capacitor [package=THT]  # not connected
  R3_2 = Resistor [resistance=10k package=THT]

nets:
  N1: Arduino1.D13, Atmel's_Atmega32L_Microchip1.connector7
  N2: Arduino1.D12, Atmel's_Atmega32L_Microchip1.connector6
  N3: Arduino1.D11, Atmel's_Atmega32L_Microchip1.connector5
  N4: Arduino1.D10, Atmel's_Atmega32L_Microchip1.connector8, R3_2.Pin_0
  N5: Arduino1.D9, LED1.anode
  N6: Arduino1.D8, LED2.anode
  N7: Arduino1.D7, LED3.anode
  N8: Arduino1.GND, R2.Pin_0
  N9: LED2.cathode, LED1.cathode, LED3.cathode, R2.Pin_1
  N10: Atmel's_Atmega32L_Microchip1.connector9, U1.input_voltage, LED4.anode, C2.-, R3_2.Pin_1
  N11: Atmel's_Atmega32L_Microchip1.connector10, U1.GND, VCC1.-, R3.Pin_0, C3.pin_1, C4.pin_0, C2.+
  N12: Atmel's_Atmega32L_Microchip1.connector11, XTAL1.pin_1, C3.pin_0
  N13: Atmel's_Atmega32L_Microchip1.connector12, XTAL1.pin_0, C4.pin_1
  N14: U1.output_voltage, VCC1.+
  N15: LED4.cathode, R3.Pin_1

notes:
  Programming leds:
  Blue: ICSP Heartbeat
  Red: Programming
  Error
  Green: Programming in
  progress
  The Proper way to bootload or program the Atmega32L.
  Using ArduinoISP
  (In avrdude, use avrisp)
  Pins:
  Arduino - Atmega32L
  10 - 9-Reset
  11 - 6-MOSI
  12 - 7-MISO
  13 - 8-SCK
