# Fritzing sketch id4134_Atmega32LBrokeOut_updated_0 (saved by Fritzing 0.4.3b)
breadboards: 4

parts:
  Atmel's_Atmega32L_Microchip1 = AVR-Atmega32
  XTAL1 = Crystal [package=THT]
  R1 = Resistor [resistance=10k package=THT]
  S1 = Pushbutton [package="[THT]"]
  Arduino1 = Arduino
  LED2 = Red LED - 5mm
  LED1 = Blue LED - 5mm
  LED3 = green LED - 5mm
  R2 = Resistor [resistance=220 package=THT]

nets:
  N1: Atmel's_Atmega32L_Microchip1.connector5, Arduino1.D11
  N2: Atmel's_Atmega32L_Microchip1.connector6, Arduino1.D12
  N3: Atmel's_Atmega32L_Microchip1.connector7, Arduino1.D13
  N4: Atmel's_Atmega32L_Microchip1.connector8, R1.Pin_0, Arduino1.D10
  N5: Atmel's_Atmega32L_Microchip1.connector9, Atmel's_Atmega32L_Microchip1.connector29, R1.Pin_1, S1.Pin_2, Arduino1.+5V
  N6: Atmel's_Atmega32L_Microchip1.connector10, Atmel's_Atmega32L_Microchip1.connector30, S1.Pin_4, Arduino1.GND, R2.Pin_0
  N7: Atmel's_Atmega32L_Microchip1.connector11, XTAL1.pin_1
  N8: Atmel's_Atmega32L_Microchip1.connector12, XTAL1.pin_0
  N9: Arduino1.D9, LED1.anode
  N10: Arduino1.D8, LED2.anode
  N11: Arduino1.D7, LED3.anode
  N12: LED2.cathode, LED1.cathode, LED3.cathode, R2.Pin_1

notes:
  RX/TX Lines / Multipurpose I/O
  AHREF
  Reset
  16mhz Oscillator
  ADC Mutipurpose I/O
  Bi-Directional I/O + JTAG Function Lines
  Multipurpose I/O
  ICSP Programming Lines
  Programming leds:
  Blue: ICSP Heartbeat
  Red: Programming
  Error
  Green: Programming in
  progress
