# Fritzing sketch id4136_The_Color_Machine_Arduino_Mega_Shield_0 (saved by Fritzing 0.7.11b)
breadboards: 2

parts:
  U1 = Arduino Mega
  J5 = Generic female header - metal rounded - 2 pins [package=THT]
  J6 = Generic female header - metal rounded - 2 pins [package=THT]
  J7 = Generic female header - metal rounded - 2 pins [package=THT]
  C1 = Electrolytic Capacitor [package=THT]
  C2 = Electrolytic Capacitor [package=THT]
  J9 = Generic female header - metal rounded - 5 pins [package=THT]
  J10 = Generic female header - metal rounded - 3 pins [package=THT]
  J11 = Generic female header - metal rounded - 5 pins [package=THT]
  J12 = Generic female header - metal rounded - 3 pins [package=THT]
  J13 = Generic female header - metal rounded - 3 pins [package=THT]
  J14 = Generic female header - metal rounded - 5 pins [package=THT]
  J17 = Generic female header - metal rounded - 2 pins [package=THT]
  J18 = Generic female header - metal rounded - 4 pins [package=THT]
  J19 = Generic female header - metal rounded - 5 pins [package=THT]
  R1 = 10k Ω Resistor [package=THT]
  R2 = 10k Ω Resistor [package=THT]
  R3 = 10k Ω Resistor [package=THT]

nets:
  N1: U1.D13, J18.pin1
  N2: U1.D12, J14.pin3
  N3: U1.D11, J14.pin2
  N4: U1.D10, J14.pin4
  N5: U1.D9, J18.pin2
  N6: U1.D8, J18.pin3
  N7: U1.D7, J18.pin4
  N8: U1.D6, J19.pin1
  N9: U1.D5, J19.pin2
  N10: U1.D4, J19.pin3
  N11: U1.D3, J19.pin4
  N12: U1.D2, J19.pin5
  N13: U1.+5V, J5.pin1, J6.pin1, J7.pin1, C1.+, C2.+, J9.pin2, J14.pin5, J17.pin2
  N14: U1.GND, C1.-, C2.-, J9.pin1, J14.pin1, J17.pin1, R1.Pin_0, R2.Pin_0, R3.Pin_0
  N15: U1.A0, J9.pin3
  N16: U1.A1, J9.pin4
  N17: U1.A2, J9.pin5
  N18: U1.A3, J5.pin2, R1.Pin_1
  N19: U1.A4, J6.pin2, R2.Pin_1
  N20: U1.A5, J7.pin2, R3.Pin_1
  N21: U1.D22, J12.pin1
  N22: U1.D23, J11.pin1, J12.pin2
  N23: U1.D24, J10.pin1
  N24: U1.D25, J10.pin2, J11.pin2
  N25: U1.D26, J13.pin1
  N26: U1.D27, J11.pin3, J13.pin2
  N27: U1.D30, J12.pin3
  N28: U1.D31, J10.pin3, J11.pin5
  N29: U1.D32, J13.pin3

notes:
  Jumper pins 23-31
  Rotary Encoder 1
  Rotary Encoder 2
  Rotary Encoder 3
  R  DB5 DB6  B  DB7
  RS  G   DB4  E
  RGB LCD SHIELD
  RGB LED STRIP
  BUTTON  1   2   3
  RGB LED RING 1
  GND  5V
  5V  GND
  GND DAT CLK LCT  5V
  GND VCC SDO CLK  LE
  COLOR MACHINE
  www.ghidiniguerrini.it
  Arduino Mega Shield
