# Fritzing sketch id4137_The_Color_Machine_LED_Ring_Shield_0 (saved by Fritzing 0.7.11b)
breadboards: 1

parts:
  J1 = Generic female header - metal rounded - 10 pins [package=THT]
  J4 = Generic female header - metal rounded - 3 pins [package=THT]
  J2 = Generic female header - metal rounded - 5 pins [package=THT]
  J3 = Generic female header - metal rounded - 5 pins [package=THT]

nets:
  N1: J1.pin1, J1.pin9, J2.pin1, J3.pin1
  N2: J1.pin2, J2.pin2, J3.pin2
  N3: J1.pin3, J4.pin3
  N4: J1.pin4, J4.pin2
  N5: J1.pin5, J4.pin1
  N6: J1.pin6, J2.pin3
  N7: J1.pin7, J2.pin4, J3.pin4
  N8: J1.pin8, J2.pin5, J3.pin5
  N9: J1.pin10, J3.pin3

notes:
  GND
  VCC
  SDI
  CLK
  LE
  OE
  SDO
  SDO > SDI
  ENCB
  SWITCH
