# Fritzing sketch id4138_The_Color_Machine_RGB_LCD_Shield_0 (saved by Fritzing 0.7.11b)
breadboards: 1

parts:
  U1 = Arduino Mega
  J6 = Generic female header - metal rounded - 18 pins [package=THT]
  R1 = Rotary Potentiometer (Small) [maximum_resistance=10kΩ]
  J3 = Generic female header - metal rounded - 5 pins [package=THT]
  J1 = Generic female header - metal rounded - 2 pins [package=THT]
  J2 = Generic female header - metal rounded - 4 pins [package=THT]

nets:
  N1: U1.D13, J6.pin4, J2.pin1
  N2: U1.D9, J6.pin17, J2.pin2
  N3: U1.D8, J6.pin11, J2.pin3
  N4: U1.D7, J6.pin6, J2.pin4
  N5: U1.D6, J6.pin16, J3.pin1
  N6: U1.D5, J6.pin12, J3.pin2
  N7: U1.D4, J6.pin13, J3.pin3
  N8: U1.D3, J6.pin18, J3.pin4
  N9: U1.D2, J6.pin14, J3.pin5
  N10: U1.+5V, J6.pin2, J6.pin15, R1.leg1, J1.pin2
  N11: U1.GND, J6.pin1, J6.pin5, R1.leg2, J1.pin1
  N12: J6.pin3, R1.wiper

notes:
  GND 5V
  Pot
  www.ghidiniguerrini.it
  RGB LCD SHIELD
  GND  5V  POT  RS GND   E                    DB4 DB5 DB6 DB7  5V   R   G   B
  DB7  B  BD6 DB5  R
  E  DB4  G  RS
