# Fritzing sketch id4139_The_Color_Machine_RGB_LED_Strip_0 (saved by Fritzing 0.7.11b)
breadboards: 3

parts:
  U1 = 74HC595 [package="DIP16 [THT]"]
  U2 = 74HC595 [package="DIP16 [THT]"]
  U4 = 74HC595 [package="DIP16 [THT]"]
  U5 = 74HC595 [package="DIP16 [THT]"]
  U6 = 74HC595 [package="DIP16 [THT]"]
  LED_1 = RGB_LED__com._anode__rbg
  LED_2 = RGB_LED__com._anode__rbg
  LED_16 = RGB_LED__com._anode__rbg
  LED_15 = RGB_LED__com._anode__rbg
  LED_14 = RGB_LED__com._anode__rbg
  LED_13 = RGB_LED__com._anode__rbg
  LED_12 = RGB_LED__com._anode__rbg
  LED_11 = RGB_LED__com._anode__rbg
  LED_3 = RGB_LED__com._anode__rbg
  LED_10 = RGB_LED__com._anode__rbg
  LED_9 = RGB_LED__com._anode__rbg
  LED_8 = RGB_LED__com._anode__rbg
  LED_7 = RGB_LED__com._anode__rbg
  LED_6 = RGB_LED__com._anode__rbg
  LED_5 = RGB_LED__com._anode__rbg
  LED_4 = RGB_LED__com._anode__rbg
  U7 = 74HC595 [package="DIP16 [THT]"]
  R1 = 470k Ω Resistor [package=THT]
  R2 = 470k Ω Resistor [package=THT]
  R5 = 470k Ω Resistor [package=THT]
  R4 = 470k Ω Resistor [package=THT]
  R3 = 470k Ω Resistor [package=THT]
  R6 = 470k Ω Resistor [package=THT]
  R7 = 470k Ω Resistor [package=THT]
  R8 = 470k Ω Resistor [package=THT]
  R13 = 470k Ω Resistor [package=THT]
  R12 = 470k Ω Resistor [package=THT]
  R10 = 470k Ω Resistor [package=THT]
  R11 = 470k Ω Resistor [package=THT]
  R9 = 470k Ω Resistor [package=THT]
  R20 = 470k Ω Resistor [package=THT]
  R19 = 470k Ω Resistor [package=THT]
  R18 = 470k Ω Resistor [package=THT]
  R28 = 470k Ω Resistor [package=THT]
  R24 = 470k Ω Resistor [package=THT]
  R23 = 470k Ω Resistor [package=THT]
  R22 = 470k Ω Resistor [package=THT]
  R25 = 470k Ω Resistor [package=THT]
  R26 = 470k Ω Resistor [package=THT]
  R21 = 470k Ω Resistor [package=THT]
  R53 = 470k Ω Resistor [package=THT]
  R27 = 470k Ω Resistor [package=THT]
  R36 = 470k Ω Resistor [package=THT]
  R32 = 470k Ω Resistor [package=THT]
  R31 = 470k Ω Resistor [package=THT]
  R30 = 470k Ω Resistor [package=THT]
  R33 = 470k Ω Resistor [package=THT]
  R34 = 470k Ω Resistor [package=THT]
  R35 = 470k Ω Resistor [package=THT]
  R29 = 470k Ω Resistor [package=THT]
  R44 = 470k Ω Resistor [package=THT]
  R40 = 470k Ω Resistor [package=THT]
  R39 = 470k Ω Resistor [package=THT]
  R38 = 470k Ω Resistor [package=THT]
  R42 = 470k Ω Resistor [package=THT]
  R41 = 470k Ω Resistor [package=THT]
  R37 = 470k Ω Resistor [package=THT]
  R43 = 470k Ω Resistor [package=THT]
  R52 = 470k Ω Resistor [package=THT]
  R48 = 470k Ω Resistor [package=THT]
  R47 = 470k Ω Resistor [package=THT]
  R46 = 470k Ω Resistor [package=THT]
  R49 = 470k Ω Resistor [package=THT]
  R50 = 470k Ω Resistor [package=THT]
  R45 = 470k Ω Resistor [package=THT]
  IN = male pin header, 5 pins [form="♂ (male)"]
  OUT = male pin header, 5 pins [form="♂ (male)"]
  C1 = Electrolytic Capacitor [package=THT]
  R54 = 10k Ω Resistor [package=THT]
  R55 = 10k Ω Resistor [package=THT]
  R56 = 10k Ω Resistor [package=THT]

nets:
  N1: U1.Q1, R2.Pin_0
  N2: U1.Q2, R3.Pin_0
  N3: U1.Q3, R4.Pin_0
  N4: U1.Q4, R5.Pin_0
  N5: U1.Q5, R6.Pin_0
  N6: U1.Q6, R7.Pin_0
  N7: U1.Q7, R8.Pin_0
  GND: U1.GND, U1.OE, U2.GND, U2.OE, U4.GND, U4.OE, U5.GND, U5.OE, U6.GND, U6.OE, LED_1.connector1, LED_2.connector1, LED_16.connector1, LED_15.connector1, LED_14.connector1, LED_13.connector1, LED_12.connector1, LED_11.connector1, LED_3.connector1, LED_10.connector1, LED_9.connector1, LED_8.connector1, LED_7.connector1, LED_6.connector1, LED_5.connector1, LED_4.connector1, U7.GND, U7.OE, IN.pin5, OUT.pin5, C1.+, R54.Pin_0, R55.Pin_0, R56.Pin_0
  N8: U1.Q7', U2.DS
  VCC: U1.MR, U1.VCC, U2.MR, U2.VCC, U4.MR, U4.VCC, U5.MR, U5.VCC, U6.MR, U6.VCC, U7.MR, U7.VCC, IN.pin1, OUT.pin1, C1.-
  N9: U1.SH_CP, U2.SH_CP, U4.SH_CP, U5.SH_CP, U6.SH_CP, U7.SH_CP, IN.pin3, OUT.pin3, R56.Pin_1
  N10: U1.ST_CP, U2.ST_CP, U4.ST_CP, U5.ST_CP, U6.ST_CP, U7.ST_CP, IN.pin2, OUT.pin2, R55.Pin_1
  N11: U1.DS, IN.pin4, R54.Pin_1
  N12: U1.Q0, R1.Pin_0
  N13: U2.Q1, R12.Pin_0
  N14: U2.Q2, R10.Pin_0
  N15: U2.Q3, R11.Pin_0
  N16: U2.Q4, R9.Pin_0
  N17: U2.Q5, R20.Pin_0
  N18: U2.Q6, R19.Pin_0
  N19: U2.Q7, R18.Pin_0
  N20: U2.Q7', U7.DS
  N21: U2.Q0, R13.Pin_0
  N22: U4.Q1, R36.Pin_0
  N23: U4.Q2, R32.Pin_0
  N24: U4.Q3, R31.Pin_0
  N25: U4.Q4, R30.Pin_0
  N26: U4.Q5, R33.Pin_0
  N27: U4.Q6, R34.Pin_0
  N28: U4.Q7, R29.Pin_0
  N29: U4.Q7', U5.DS
  N30: U4.DS, U7.Q7'
  N31: U4.Q0, R27.Pin_0
  N32: U5.Q1, R44.Pin_0
  N33: U5.Q2, R40.Pin_0
  N34: U5.Q3, R39.Pin_0
  N35: U5.Q4, R38.Pin_0
  N36: U5.Q5, R41.Pin_0
  N37: U5.Q6, R42.Pin_0
  N38: U5.Q7, R37.Pin_0
  N39: U5.Q7', U6.DS
  N40: U5.Q0, R35.Pin_0
  N41: U6.Q1, R52.Pin_0
  N42: U6.Q2, R48.Pin_0
  N43: U6.Q3, R47.Pin_0
  N44: U6.Q4, R46.Pin_0
  N45: U6.Q5, R49.Pin_0
  N46: U6.Q6, R50.Pin_0
  N47: U6.Q7, R45.Pin_0
  N48: U6.Q7', OUT.pin4
  N49: U6.Q0, R43.Pin_0
  N50: LED_1.connector0, R1.Pin_1
  N51: LED_1.connector2, R2.Pin_1
  N52: LED_1.connector3, R3.Pin_1
  N53: LED_2.connector0, R4.Pin_1
  N54: LED_2.connector2, R5.Pin_1
  N55: LED_2.connector3, R6.Pin_1
  N56: LED_16.connector0, R49.Pin_1
  N57: LED_16.connector2, R50.Pin_1
  N58: LED_16.connector3, R45.Pin_1
  N59: LED_15.connector0, R48.Pin_1
  N60: LED_15.connector2, R47.Pin_1
  N61: LED_15.connector3, R46.Pin_1
  N62: LED_14.connector0, R37.Pin_1
  N63: LED_14.connector2, R43.Pin_1
  N64: LED_14.connector3, R52.Pin_1
  N65: LED_13.connector0, R38.Pin_1
  N66: LED_13.connector2, R41.Pin_1
  N67: LED_13.connector3, R42.Pin_1
  N68: LED_12.connector0, R44.Pin_1
  N69: LED_12.connector2, R40.Pin_1
  N70: LED_12.connector3, R39.Pin_1
  N71: LED_11.connector0, R34.Pin_1
  N72: LED_11.connector2, R29.Pin_1
  N73: LED_11.connector3, R35.Pin_1
  N74: LED_3.connector0, R7.Pin_1
  N75: LED_3.connector2, R8.Pin_1
  N76: LED_3.connector3, R13.Pin_1
  N77: LED_10.connector0, R31.Pin_1
  N78: LED_10.connector2, R30.Pin_1
  N79: LED_10.connector3, R33.Pin_1
  N80: LED_9.connector0, R27.Pin_1
  N81: LED_9.connector2, R36.Pin_1
  N82: LED_9.connector3, R32.Pin_1
  N83: LED_8.connector0, R26.Pin_1
  N84: LED_8.connector2, R21.Pin_1
  N85: LED_8.connector3, R53.Pin_1
  N86: LED_7.connector0, R23.Pin_1
  N87: LED_7.connector2, R22.Pin_1
  N88: LED_7.connector3, R25.Pin_1
  N89: LED_6.connector0, R18.Pin_1
  N90: LED_6.connector2, R28.Pin_1
  N91: LED_6.connector3, R24.Pin_1
  N92: LED_5.connector0, R9.Pin_1
  N93: LED_5.connector2, R20.Pin_1
  N94: LED_5.connector3, R19.Pin_1
  N95: LED_4.connector0, R12.Pin_1
  N96: LED_4.connector2, R10.Pin_1
  N97: LED_4.connector3, R11.Pin_1
  N98: U7.Q1, R24.Pin_0
  N99: U7.Q2, R23.Pin_0
  N100: U7.Q3, R22.Pin_0
  N101: U7.Q4, R25.Pin_0
  N102: U7.Q5, R26.Pin_0
  N103: U7.Q6, R21.Pin_0
  N104: U7.Q7, R53.Pin_0
  N105: U7.Q0, R28.Pin_0

notes:
  GND
  LTC
  CLK
  DAT
  5V
  RLS
  RGB LED Strip
  +5V
  www.ghidiniguerrini.it
