# Fritzing sketch id413_wccontroller_0 (saved by Fritzing 0.9.0b)
breadboards: 1

parts:
  12V_Supply = molex pin header, 2 pins [form=molex]
  RE1 = Bourns_PEC11-4xxxK-Sxxxx_Rotary_Encoder.fzp
  Q1 = MOSFET-NCHANNEL [part_number=IRL510N package=to220v]
  R1 = Temperature Sensor (Thermistor) [thermistor_type=NTC package=THT]
  R2 = Temperature Sensor (Thermistor) [thermistor_type=NTC package=THT]
  R3 = Temperature Sensor (Thermistor) [thermistor_type=NTC package=THT]
  R4 = Resistor [tolerance=±5% resistance=10k package=THT]
  Amb = male pin header, 2 pins [form="♂ (male)"]
  Water2 = male pin header, 2 pins [form="♂ (male)"]
  Water1 = male pin header, 2 pins [form="♂ (male)"]
  Q2 = MOSFET-NCHANNEL [part_number=IRL510N package=to220v]
  Case = male pin header, 2 pins [form="♂ (male)"]
  R5 = Resistor [tolerance=±5% resistance=10k package=THT]
  R6 = Resistor [tolerance=±5% resistance=10k package=THT]
  R7 = Resistor [tolerance=±5% resistance=10k package=THT]
  R8 = Temperature Sensor (Thermistor) [thermistor_type=NTC package=THT]
  DISPLAY_-_I2C_Used = LCD-16X2 [package=lcd-16x2]
  LCD = male pin header, 4 pins [form="♂ (male)"]
  Encoder = female pin header, 5 pins [form="♀ (female)"]
  Fan1 = male pin header, 3 pins [form="♂ (male)"]
  Fan2 = male pin header, 3 pins [form="♂ (male)"]
  Fan3 = male pin header, 4 pins [form="♂ (male)"]
  Part2 = Arduino Micro (Rev3)

nets:
  N1: 12V_Supply.pin1, Fan1.pin1, Fan2.pin1, Fan3.pin2, Part2.VIN
  N2: 12V_Supply.pin2, RE1.connector1, Q1.S, R4.Pin_1, Q2.S, R5.Pin_1, R6.Pin_1, R7.Pin_1, DISPLAY_-_I2C_Used.K, LCD.pin1, Encoder.pin2, Fan3.pin1, Part2.GND
  N3: RE1.connector0, Encoder.pin1, Part2.D12_PWM/A11
  N4: RE1.connector2, Encoder.pin3, Part2.D9_PWM/A9
  N5: RE1.connector3, Encoder.pin4, Part2.D8_PWM/A8
  N6: RE1.connector4, R1.pin_1, R2.pin_1, R3.pin_1, Amb.pin2, Water2.pin2, Water1.pin2, Case.pin2, R8.pin_1, DISPLAY_-_I2C_Used.A, LCD.pin2, Encoder.pin5, Part2.5V
  N7: Q1.G, Part2.D3/SCL
  N8: Q1.D, Fan1.pin2
  N9: R1.pin_0, R4.Pin_0, Amb.pin1, Part2.A0
  N10: R2.pin_0, Water2.pin1, R5.Pin_0, Part2.A1
  N11: R3.pin_0, Water1.pin1, R6.Pin_0, Part2.A2
  N12: Q2.G, Part2.D5_PWM
  N13: Q2.D, Fan2.pin2
  N14: Case.pin1, R7.Pin_0, R8.pin_0, Part2.A3
  N15: DISPLAY_-_I2C_Used.DB6, LCD.pin4, Part2.A4
  N16: DISPLAY_-_I2C_Used.DB7, LCD.pin3, Part2.A5
  N17: Fan3.pin4, Part2.D6_PWM/A7
