# Fritzing sketch id4141_basic_led_hookup_0 (saved by Fritzing 0.9.2b)
breadboards: 1

parts:
  Part1 = Arduino Uno (Rev3)
  LED2 = LED - 5mm [color="Red (633nm)" package="5 mm [THT]"]
  R1 = Resistor [tolerance=±5% resistance=220 package=THT]
  LED4 = LED - 5mm [color="Red (633nm)" package="5 mm [THT]"]
  R2 = Resistor [tolerance=±5% resistance=220 package=THT]

nets:
  N1: Part1.D8, LED2.anode, LED4.anode
  N2: Part1.GND, R1.Pin_0
  N3: LED2.cathode, R1.Pin_1
  N4: LED4.cathode, R2.Pin_0
