# Fritzing sketch id4142_finalFritz_0 (saved by Fritzing 0.9.2b)
breadboards: 1

parts:
  LED1 = LED - 5mm [color="Red (633nm)" package="5 mm [THT]"]
  LED2 = LED - 5mm [color="Red (633nm)" package="5 mm [THT]"]
  LED3 = LED - 5mm [color="Red (633nm)" package="5 mm [THT]"]
  R1 = Resistor [tolerance=±5% resistance=220 package=THT]
  Part1 = Arduino Uno (Rev3)
  R2 = Resistor [tolerance=±5% resistance=220 package=THT]
  R3 = Resistor [tolerance=±5% resistance=220 package=THT]
  LED4 = LED - 5mm [color="Red (633nm)" package="5 mm [THT]"]
  LED5 = LED - 5mm [color="Red (633nm)" package="5 mm [THT]"]
  LED6 = LED - 5mm [color="Red (633nm)" package="5 mm [THT]"]
  LED7 = LED - 5mm [color="Red (633nm)" package="5 mm [THT]"]
  R4 = Resistor [tolerance=±5% resistance=220 package=THT]
  LED8 = LED - 5mm [color="Red (633nm)" package="5 mm [THT]"]
  LED9 = LED - 5mm [color="Red (633nm)" package="5 mm [THT]"]
  R5 = Resistor [tolerance=±5% resistance=220 package=THT]
  LED10 = LED - 5mm [color="Red (633nm)" package="5 mm [THT]"]
  LED11 = LED - 5mm [color="Red (633nm)" package="5 mm [THT]"]
  R6 = Resistor [tolerance=±5% resistance=220 package=THT]
  LED12 = LED - 5mm [color="Red (633nm)" package="5 mm [THT]"]
  LED13 = LED - 5mm [color="Red (633nm)" package="5 mm [THT]"]
  R7 = Resistor [tolerance=±5% resistance=220 package=THT]
  LED14 = LED - 5mm [color="Red (633nm)" package="5 mm [THT]"]
  LED15 = LED - 5mm [color="Red (633nm)" package="5 mm [THT]"]
  LED16 = LED - 5mm [color="Red (633nm)" package="5 mm [THT]"]
  LED17 = LED - 5mm [color="Red (633nm)" package="5 mm [THT]"]
  LED18 = LED - 5mm [color="Red (633nm)" package="5 mm [THT]"]
  LED19 = LED - 5mm [color="Red (633nm)" package="5 mm [THT]"]
  LED20 = LED - 5mm [color="Red (633nm)" package="5 mm [THT]"]
  LED21 = LED - 5mm [color="Red (633nm)" package="5 mm [THT]"]
  LED22 = LED - 5mm [color="Red (633nm)" package="5 mm [THT]"]
  LED23 = LED - 5mm [color="Red (633nm)" package="5 mm [THT]"]
  LED24 = LED - 5mm [color="Red (633nm)" package="5 mm [THT]"]
  LED25 = LED - 5mm [color="Red (633nm)" package="5 mm [THT]"]
  LED26 = LED - 5mm [color="Red (633nm)" package="5 mm [THT]"]
  LED27 = LED - 5mm [color="Red (633nm)" package="5 mm [THT]"]
  R8 = Resistor [tolerance=±5% resistance=220 package=THT]
  R9 = Resistor [tolerance=±5% resistance=220 package=THT]
  R10 = Resistor [tolerance=±5% resistance=220 package=THT]
  R11 = Resistor [tolerance=±5% resistance=220 package=THT]
  R12 = Resistor [tolerance=±5% resistance=220 package=THT]
  R13 = Resistor [tolerance=±5% resistance=220 package=THT]
  S1 = Pushbutton [package="[THT]"]
  R14 = Resistor [tolerance=±5% resistance=220 package=THT]

nets:
  N1: LED1.cathode, R1.Pin_1, LED5.cathode
  N2: LED1.anode, Part1.D7, LED5.anode, LED22.anode, LED23.anode
  N3: LED2.cathode, R2.Pin_1, LED6.cathode
  N4: LED2.anode, Part1.D8, LED6.anode, LED20.anode, LED21.anode
  N5: LED3.cathode, R3.Pin_1, LED7.cathode, LED15.cathode
  N6: LED3.anode, Part1.D9_PWM, LED7.anode, LED15.anode, LED18.anode
  N7: R1.Pin_0, Part1.GND, R2.Pin_0, R3.Pin_0, R4.Pin_0, R5.Pin_0, R6.Pin_0, R7.Pin_1, R8.Pin_1, R9.Pin_1, R10.Pin_1, R11.Pin_1, R12.Pin_1, R13.Pin_1, S1.Pin_1, S1.Pin_2
  N8: Part1.D10_PWM/SS, LED4.anode, LED8.anode, LED16.anode
  N9: Part1.D11_PWM/MOSI, LED9.anode, LED10.anode, LED17.anode, LED19.anode
  N10: Part1.D12/MISO, LED11.anode, LED12.anode, LED24.anode, LED25.anode
  N11: Part1.D13/SCK, LED13.anode, LED14.anode, LED26.anode, LED27.anode
  N12: Part1.D2, S1.Pin_3, S1.Pin_4, R14.Pin_0
  N13: Part1.5V, R14.Pin_1
  N14: LED4.cathode, R4.Pin_1, LED8.cathode, LED16.cathode
  N15: LED9.cathode, R5.Pin_1, LED10.cathode, LED17.cathode
  N16: LED11.cathode, R6.Pin_1, LED12.cathode
  N17: LED13.cathode, R7.Pin_0, LED14.cathode
  N18: LED18.cathode, R10.Pin_0
  N19: LED19.cathode, R11.Pin_0
  N20: LED20.cathode, LED21.cathode, R9.Pin_0
  N21: LED22.cathode, LED23.cathode, R8.Pin_0
  N22: LED24.cathode, LED25.cathode, R12.Pin_0
  N23: LED26.cathode, LED27.cathode, R13.Pin_0
