# Fritzing sketch id4143_The_Kitt_eyes_with_button_0 (saved by Fritzing 0.9.2b)
breadboards: 1

parts:
  Componente1 = Arduino Uno (Rev3)
  LED1 = smd LED [color="Red (633nm)" package="0603 [SMD]"]  # not connected
  LED2 = smd LED [color="Red (633nm)" package="0603 [SMD]"]  # not connected
  LED3 = smd LED [color="Red (633nm)" package="0603 [SMD]"]  # not connected
  LED4 = smd LED [color="Red (633nm)" package="0603 [SMD]"]  # not connected
  LED5 = smd LED [color="Red (633nm)" package="0603 [SMD]"]  # not connected
  LED6 = smd LED [color="Red (633nm)" package="0603 [SMD]"]  # not connected
  LED7 = smd LED [color="Red (633nm)" package="0603 [SMD]"]  # not connected
  LED8 = smd LED [color="Red (633nm)" package="0603 [SMD]"]  # not connected
  LED9 = smd LED [color="Red (633nm)" package="0603 [SMD]"]  # not connected
  LED10 = smd LED [color="Red (633nm)" package="0603 [SMD]"]  # not connected
  S1 = Pushbutton [package="[THT]"]
  R1 = Resistor [tolerance=±5% resistance=10k package="0805 [SMD]"]
  S2 = Pushbutton [package="[THT]"]
  R2 = Resistor [tolerance=±5% resistance=10k package="0805 [SMD]"]

nets:
  N1: Componente1.D2, R2.Pin_0
  N2: Componente1.D3_PWM, R1.Pin_0
  N3: Componente1.GND, R1.Pin_1, R2.Pin_1
  N4: S1.Pin_1, S1.Pin_2
  N5: S1.Pin_3, S1.Pin_4
  N6: S2.Pin_1, S2.Pin_2
  N7: S2.Pin_3, S2.Pin_4
