# Fritzing sketch id4144_Midterm_LED__0 (saved by Fritzing 0.9.2b)
breadboards: 1

parts:
  Raspberry_Pi1 = Raspberry Pi 2  # not connected
  R1 = Resistor [tolerance=±5% resistance=220 package=THT]
  R2 = Resistor [tolerance=±5% resistance=220 package=THT]
  R3 = Resistor [tolerance=±5% resistance=220 package=THT]
  R4 = Resistor [tolerance=±5% resistance=220 package=THT]
  LED1 = LED - 5mm [color="Red (633nm)" package="5 mm [THT]"]
  LED2 = LED - 5mm [color="Red (633nm)" package="5 mm [THT]"]
  LED4 = LED - 5mm [color="Red (633nm)" package="5 mm [THT]"]
  LED5 = LED - 5mm [color="Red (633nm)" package="5 mm [THT]"]
  J4 = T Cobbler Plus Cable

nets:
  N1: R1.Pin_0, R2.Pin_0, R3.Pin_1, R4.Pin_0
  N2: R1.Pin_1, LED1.anode, J4.connector14
  N3: R2.Pin_1, LED2.anode, J4.connector36
  N4: R3.Pin_0, LED4.anode, J4.connector39
  N5: R4.Pin_1, LED5.anode, J4.connector6, J4.connector24
  N6: LED1.cathode, LED2.cathode, LED4.cathode, LED5.cathode
