# Fritzing sketch id4145_saved_0 (saved by Fritzing 0.9.3b)
breadboards: 1

parts:
  Part1 = Arduino Color LCD Shield
  Part2 = Arduino Leonardo (Rev3b)
  Part3 = Lilypad Power Supply  # not connected
  Digital_Panel_Meter_Voltage_DMS-20PC_by_Murata1 = Digital Panel Meter, Voltage, DMS-20PC
  JP1 = RCA [package=rca_lock]
  JP2 = Header 5x2 [package=2x5-shrouded_smd]

nets:
  N1: Part1.D0, Part2.D0/RX
  N2: Part1.AREF, Digital_Panel_Meter_Voltage_DMS-20PC_by_Murata1.1:_VCC
  N3: Part1.GND, Digital_Panel_Meter_Voltage_DMS-20PC_by_Murata1.5:_#DP2
  N4: Part1.D13, Digital_Panel_Meter_Voltage_DMS-20PC_by_Murata1.2:_ENABLE
  N5: Part1.D12, Digital_Panel_Meter_Voltage_DMS-20PC_by_Murata1.6:_#DP1
  N6: Part1.D11, Digital_Panel_Meter_Voltage_DMS-20PC_by_Murata1.3:_GND, Digital_Panel_Meter_Voltage_DMS-20PC_by_Murata1.4:_#DP3
  N7: Part1.RESET, Part2.n.c.
  N8: Part2.IOREF, Digital_Panel_Meter_Voltage_DMS-20PC_by_Murata1.11:_(+)_INPUT_HI
  N9: Part2.3V3, Digital_Panel_Meter_Voltage_DMS-20PC_by_Murata1.10:_Analog_Common
  N10: Part2.GND, Digital_Panel_Meter_Voltage_DMS-20PC_by_Murata1.8:_Reference_Out, Digital_Panel_Meter_Voltage_DMS-20PC_by_Murata1.9:_Display_Test/Hold
  N11: Part2.VIN, Digital_Panel_Meter_Voltage_DMS-20PC_by_Murata1.7:_Reference_In
  N12: Part2.A0, JP2.5, JP2.6
  N13: Part2.A1, JP1.PIN
  N14: Part2.A4, JP2.1, JP2.2
  N15: Part2.A5, JP1.SHELL
  N16: Part2.D11_PWM, JP1.SWITCH
  N17: JP2.3, JP2.4
  N18: JP2.7, JP2.8
  N19: JP2.9, JP2.10
