# Fritzing sketch id4147_Untitled_Sketch_0 (saved by Fritzing 0.9.3b)
breadboards: 1

parts:
  V1 = DC Power [voltage=7.4V]
  C1 = Electrolytic Capacitor [capacitance=100μF package="0807 [SMD, electrolytic]"]
  C2 = Electrolytic Capacitor [capacitance=47µF package="0807 [SMD, electrolytic]"]
  C3 = Ceramic Capacitor [capacitance=0.1µF package="200 mil [THT, multilayer]"]
  Q1 = TRANSISTOR_NPN [package=sot23]
  R1 = Resistor [tolerance=±5% resistance=39k package="1206 [SMD]"]
  R2 = Resistor [tolerance=±5% resistance=1k package="1206 [SMD]"]
  R3 = Resistor [tolerance=±5% resistance=470 package="1206 [SMD]"]
  R4 = Resistor [tolerance=±5% resistance=10k package="1206 [SMD]"]
  C4 = Ceramic Capacitor [capacitance=10nF package="200 mil [THT, multilayer]"]
  C5 = Ceramic Capacitor [capacitance=10nF package="200 mil [THT, multilayer]"]
  C6 = Ceramic Capacitor [capacitance=1pF package="200 mil [THT, multilayer]"]
  L1 = Inductor [inductance=906.6µH package="0805 [SMD]"]
  V2 = DC Power [voltage=5V]
  Part2 = Arduino Mega 2560 (Rev3)
  Part3 = Arduino BT

nets:
  N1: V1.V+, C1.+, C2.+, C3.1, R1.Pin_1, L1.pin_0, Part2.D47
  GND: V1.V-, C1.-, V2.V-, Part2.GND, Part3.GND
  N2: Q1.B, R1.Pin_0, R4.Pin_1, C5.1
  N3: Q1.E, R3.Pin_1, C4.0
  N4: Q1.C, R2.Pin_0
  N5: R3.Pin_0, R4.Pin_0
  N6: C5.0, C6.0, L1.pin_1
  VIN: V2.V+, Part2.VIN, Part3.VIN
  N7: Part2.D0_RX0, Part3.TX/D1
  N8: Part2.D1_TX0, Part3.RX/D0
