# Fritzing sketch id4148_Halloween_Prototype_0 (saved by Fritzing 0.9.3b)
breadboards: 2

parts:
  Part1 = Arduino Uno (Rev3)
  LCD1 = LCD screen
  R1 = TRIMPOT [package=3386u]
  hc-sr1 = hc-sr04
  J1 = Piezo Speaker

nets:
  N1: Part1.D9_PWM, hc-sr1.Trig
  N2: Part1.D10_PWM/SS, hc-sr1.Echo
  N3: Part1.D11_PWM/MOSI, LCD1.E
  N4: Part1.D12/MISO, LCD1.RS
  N5: Part1.D2, LCD1.DB7
  N6: Part1.D3_PWM, LCD1.DB6
  N7: Part1.D4, LCD1.DB5
  N8: Part1.D5_PWM, LCD1.DB4
  5V: Part1.5V, LCD1.VDD, LCD1.LED+, R1.CW, hc-sr1.VCC, J1.pin2
  GND: Part1.GND, LCD1.VSS, LCD1.R/W, LCD1.LED-, R1.CCW, hc-sr1.GND, J1.pin1
  N9: LCD1.V0, R1.WIPER
