# Fritzing sketch id4149_disconnect_0 (saved by Fritzing 0.9.2b)
circuit board: 4.35825cm x 3.42441cm

parts:
  U3 = RJ45 Jack [package=rj45-8]
  J1 = female pin header, 8 pins [form="♀ (female)"]

nets:
  N1: U3.1, J1.pin7
  N2: U3.2, J1.pin6
  N3: U3.3, J1.pin8
  N4: U3.4, J1.pin5
  N5: U3.5, J1.pin1
  N6: U3.6, J1.pin4
  N7: U3.7, J1.pin2
  N8: U3.8, J1.pin3
