# Fritzing sketch id4150_MMA_1 (saved by Fritzing 0.7.7b)
breadboards: 1

parts:
  R1 = Resistor [tolerance=±1% resistance=10k power=500mW package=THT]
  Arduino1 = Arduino
  J1 = Basic Force Sensing Resistor (FSR) [package=THT]

nets:
  N1: R1.Pin_0, Arduino1.A0, J1.pin_1
  N2: R1.Pin_1, Arduino1.GND
  N3: Arduino1.+5V, J1.pin_0
