# Fritzing sketch id4150_TrafficLight_Mini_Auto_V9_Make1_0 (saved by Fritzing 0.9.2b)
breadboards: 1

parts:
  Arduino1 = Arduino Uno (Rev3)
  D8 = Rectifier Diode [part_number=1N4001 package="300 mil [THT]"]
  D9 = Rectifier Diode [part_number=1N4001 package="300 mil [THT]"]
  D10 = Rectifier Diode [part_number=1N4001 package="300 mil [THT]"]
  D11 = Rectifier Diode [part_number=1N4001 package="300 mil [THT]"]
  D12 = Rectifier Diode [part_number=1N4001 package="300 mil [THT]"]
  D13 = Rectifier Diode [part_number=1N4001 package="300 mil [THT]"]
  D14 = Rectifier Diode [part_number=1N4001 package="300 mil [THT]"]
  LED25 = LED - 5mm [color="Red (633nm)" package="5 mm [THT]"]
  LED27 = LED - 5mm [color="Red (633nm)" package="5 mm [THT]"]
  LED28 = LED - 5mm [color="Red (633nm)" package="5 mm [THT]"]
  LED29 = LED - 5mm [color="Red (633nm)" package="5 mm [THT]"]
  LED35 = LED - 5mm [color="Red (633nm)" package="5 mm [THT]"]
  LED41 = LED - 5mm [color="Yellow (585nm)" package="5 mm [THT]"]
  LED43 = LED - 5mm [color="Green (555nm)" package="5 mm [THT]"]
  LED47 = LED - 5mm [color="Yellow (585nm)" package="5 mm [THT]"]
  LED48 = LED - 5mm [color="Yellow (585nm)" package="5 mm [THT]"]
  LED49 = LED - 5mm [color="Red (633nm)" package="5 mm [THT]"]
  LED50 = LED - 5mm [color="Red (633nm)" package="5 mm [THT]"]
  LED51 = LED - 5mm [color="Red (633nm)" package="5 mm [THT]"]
  LED53 = LED - 5mm [color="Yellow (585nm)" package="5 mm [THT]"]
  LED54 = LED - 5mm [color="Green (555nm)" package="5 mm [THT]"]
  LED55 = LED - 5mm [color="Green (555nm)" package="5 mm [THT]"]
  LED56 = LED - 5mm [color="Green (555nm)" package="5 mm [THT]"]
  LED57 = LED - 5mm [color="Green (555nm)" package="5 mm [THT]"]
  LED58 = LED - 5mm [color="Green (555nm)" package="5 mm [THT]"]
  LED59 = LED - 5mm [color="Green (555nm)" package="5 mm [THT]"]
  LED61 = LED - 5mm [color="Yellow (585nm)" package="5 mm [THT]"]
  LED67 = LED - 5mm [color="Green (555nm)" package="5 mm [THT]"]
  LED68 = LED - 5mm [color="Yellow (585nm)" package="5 mm [THT]"]
  LED69 = LED - 5mm [color="Yellow (585nm)" package="5 mm [THT]"]
  LED70 = LED - 5mm [color="Yellow (585nm)" package="5 mm [THT]"]
  S1 = Pushbutton [package="[THT]"]
  R1 = Resistor [tolerance=±5% resistance=10k package=THT]

nets:
  N1: Arduino1.GND, D8.cathode
  N2: Arduino1.D2, S1.Pin_3, S1.Pin_4, R1.Pin_0
  N3: Arduino1.D3_PWM, LED25.cathode, LED27.cathode, LED28.cathode, LED29.cathode, LED35.cathode, LED49.cathode, LED50.cathode, LED51.cathode
  N4: Arduino1.D4, LED41.cathode, LED47.cathode, LED48.cathode, LED53.cathode, LED61.cathode, LED68.cathode, LED69.cathode, LED70.cathode
  N5: Arduino1.D5_PWM, LED43.cathode, LED54.cathode, LED55.cathode, LED56.cathode, LED57.cathode, LED58.cathode, LED59.cathode, LED67.cathode
  N6: Arduino1.5V, S1.Pin_1, S1.Pin_2
  N7: D8.anode, D9.cathode, D10.cathode, D11.cathode, D12.cathode, D13.cathode, D14.cathode, R1.Pin_1
  N8: D9.anode, LED61.anode, LED68.anode, LED69.anode, LED70.anode
  N9: D10.anode, LED27.anode, LED29.anode, LED49.anode, LED50.anode
  N10: D11.anode, LED41.anode, LED47.anode, LED48.anode, LED53.anode
  N11: D12.anode, LED25.anode, LED28.anode, LED35.anode, LED51.anode
  N12: D13.anode, LED56.anode, LED57.anode, LED58.anode, LED59.anode
  N13: D14.anode, LED43.anode, LED54.anode, LED55.anode, LED67.anode

notes:
  To go into Emergency Mode: Hold the Emergency Button and press RESET
  <-Emergency
