# Fritzing sketch id4151_Theremin_1b_0 (saved by Fritzing 0.9.2b)
breadboards: 1

parts:
  Batterij = Battery block 9V
  CD40106 = Hex Inverter Schmitt Trigger SN74HC14 [package="DIP (Dual Inline)"]
  Condensator = Ceramic Capacitor [capacitance=100nF package="100 mil [THT, multilayer]"]
  Weerstand = Photocell (LDR) [package=THT]
  Audio_plug = RCA [package=rca_lock]

nets:
  N1: Batterij.-, CD40106.GND, Condensator.0, Audio_plug.SWITCH
  N2: Batterij.+, CD40106.VCC
  N3: CD40106.1A, Condensator.1, Weerstand.pin_0
  N4: CD40106.1Y, Weerstand.pin_1, Audio_plug.PIN
