# Fritzing sketch id4152_theremin_and_visualizer_0 (saved by Fritzing 0.9.2b)
breadboards: 1

parts:
  Part1 = Arduino Uno (Rev3)
  MIC2 = sound sensor
  LED1 = LEDs [package=led10mm]
  LED2 = LEDs [package=led10mm]
  R1 = Resistor [tolerance=±5% resistance=220 package=THT]
  R2 = Resistor [tolerance=±5% resistance=220 package=THT]
  R3 = PHOTOCELL [package=photocell-kit]
  R4 = PHOTOCELL [package=photocell-kit]
  R5 = Resistor [tolerance=±5% resistance=220 package=THT]
  R6 = Resistor [tolerance=±5% resistance=220 package=THT]
  U1 = 2.5mm Audio Jack [package=stereojack2.5mm_stereojack2.5mm]

nets:
  N1: Part1.A0, Part1.GND, Part1.D0/RX, MIC2.connector4, R1.Pin_1, R2.Pin_1, U1.SLEEVE
  N2: Part1.A1, R5.Pin_1
  N3: Part1.A2, R6.Pin_1
  N4: Part1.D1/TX, LED1.A
  N5: Part1.D2, LED2.A
  N6: Part1.D6_PWM, U1.LEFT
  N7: Part1.D7, U1.RIGHT
  N8: Part1.5V, MIC2.connector3, R3.P$2, R4.P$2
  N9: R3.P$1, R5.Pin_0
  N10: R4.P$1, R6.Pin_0
