# Fritzing sketch id4153_rave_theremin_0 (saved by Fritzing 0.9.3b)
breadboards: 1

parts:
  Componente1 = Arduino Uno (Rev3)
  MIC1 = Microphone
  LED1 = RGB LED (com. cathode, rgb) [package="5 mm [THT]"]
  R1 = Resistor [tolerance=±5% resistance=10k package=THT]
  R2 = Photocell (LDR) [package=THT]
  R3 = Resistor [tolerance=±5% resistance=220 package=THT]
  R4 = Resistor [tolerance=±5% resistance=220 package=THT]
  R5 = Resistor [tolerance=±5% resistance=220 package=THT]

nets:
  N1: Componente1.D8, MIC1.pin2
  N2: Componente1.D9_PWM, R4.Pin_1
  N3: Componente1.D10_PWM/SS, R5.Pin_1
  N4: Componente1.D11_PWM/MOSI, R3.Pin_1
  N5: Componente1.GND, MIC1.pin1, LED1.green_anode, R1.Pin_0
  N6: Componente1.5V, R2.pin_1
  N7: LED1.red_anode, R4.Pin_0
  N8: LED1.common_cathode, R5.Pin_0
  N9: LED1.blue_anode, R3.Pin_0
