# Fritzing sketch id4154_Act_8_0 (saved by Fritzing 0.9.3b)
breadboards: 1

parts:
  LCM1602_IIC1 = generic_ic_dip_22_300mil.fzp [part_number="LCM1602 IIC" chip_label="LCM1602 IIC"]
  LCD2 = LCD screen
  Part1 = Arduino Uno (Rev3)
  T1 = LM35 Temperature Sensor [package="TO92 [THT]"]

nets:
  N1: LCM1602_IIC1.connector0, LCD2.VSS
  N2: LCM1602_IIC1.connector1, LCD2.VDD
  N3: LCM1602_IIC1.connector2, LCD2.V0
  N4: LCM1602_IIC1.connector3, LCD2.RS
  N5: LCM1602_IIC1.connector4, LCD2.R/W
  N6: LCM1602_IIC1.connector5, LCD2.E
  N7: LCM1602_IIC1.connector6, LCD2.DB0
  N8: LCM1602_IIC1.connector7, LCD2.DB1
  N9: LCM1602_IIC1.connector8, LCD2.DB2
  N10: LCM1602_IIC1.connector9, LCD2.DB3
  N11: LCM1602_IIC1.connector10, LCD2.DB4
  N12: LCM1602_IIC1.connector11, LCD2.DB5
  N13: LCM1602_IIC1.connector12, LCD2.DB6
  N14: LCM1602_IIC1.connector13, LCD2.DB7
  N15: LCM1602_IIC1.connector14, LCD2.LED+
  N16: LCM1602_IIC1.connector15, LCD2.LED-
  GND: LCM1602_IIC1.connector16, Part1.GND, T1.GND
  N17: LCM1602_IIC1.connector17, Part1.5V, T1.+Vs
  N18: LCM1602_IIC1.connector18, Part1.A4/SDA
  N19: LCM1602_IIC1.connector19, Part1.A5/SCL
  N20: Part1.A0, T1.Vout
