# Fritzing sketch id4155_thermistor_schematic_0 (saved by Fritzing 0.9.0b)
breadboards: 1

parts:
  Part1 = Arduino Uno (Rev3)
  R1 = Temperature Sensor (Thermistor) [thermistor_type=NTC package=THT]
  R2 = Resistor [tolerance=±5% resistance=10k package=THT]

nets:
  N1: Part1.A0, R1.pin_0, R2.Pin_1
  N2: Part1.GND, R2.Pin_0
  N3: Part1.5V, R1.pin_1

notes:
  Components REQD.:
  1) Arduino UNO
  2) Solderless Breadboard
  3) 10 kOhm Thermistor
  4) 10 kOhm Resistance
  5) Jumper Wires
