# Fritzing sketch id4156_Thermocouple_0 (saved by Fritzing 0.9.3b)

parts:
  Main = Arduino Uno (Rev3) [part_number=1]
  LCD1 = LCD screen [part_number=2]
  U1 = POT [package=pot_alpha_rv16af-20]
  U2 = MAX6675 [package=so08]

nets:
  N1: Main.D8, U2.SCK
  N2: Main.D11_PWM/MOSI, LCD1.E
  N3: Main.D12/MISO, LCD1.RS
  N4: Main.D2, LCD1.DB7
  N5: Main.D3_PWM, LCD1.DB6
  N6: Main.D4, LCD1.DB5
  N7: Main.D5_PWM, LCD1.DB4
  N8: Main.D6_PWM, U2.MISO
  N9: Main.D7, U2.CS
  N10: LCD1.VSS, U1.A
  N11: LCD1.VDD, U1.E
  N12: LCD1.V0, U1.S

notes:
  **Pin 2 and 3 requires a type K Thermocopule (TC) sensor**
  Pin 2: TC minus input
  Pin 3: TC plus input
