# Fritzing sketch id415_FritzingBP_0 (saved by Fritzing 0.9.1b)
breadboards: 1

parts:
  Part1 = Arduino Uno (Rev3)
  R1 = Resistor [tolerance=±5% resistance=220 package=THT]
  R2 = Resistor [tolerance=±5% resistance=220 package=THT]
  R3 = Resistor [tolerance=±5% resistance=220 package=THT]
  R4 = Resistor [tolerance=±5% resistance=220 package=THT]
  R5 = Resistor [tolerance=±5% resistance=220 package=THT]
  R6 = Resistor [tolerance=±5% resistance=220 package=THT]
  R7 = Resistor [tolerance=±5% resistance=220 package=THT]
  R8 = Resistor [tolerance=±5% resistance=220 package=THT]
  R9 = Resistor [tolerance=±5% resistance=220 package=THT]
  J2 = Piezo Speaker
  LED1 = smd LED [color="Red (633nm)" package="0805 [SMD]"]
  U2 = TOUCH [package=touch1]
  U3 = TOUCH [package=touch1]
  U4 = TOUCH [package=touch1]
  U5 = TOUCH [package=touch1]
  U6 = TOUCH [package=touch1]
  U7 = TOUCH [package=touch1]
  U8 = TOUCH [package=touch1]
  U9 = TOUCH [package=touch1]
  U10 = TOUCH [package=touch1]

nets:
  N1: Part1.D8, R4.Pin_0, U5.T2
  N2: Part1.D9_PWM, R3.Pin_0, U8.T2
  N3: Part1.D10_PWM/SS, R2.Pin_0, U9.T2
  N4: Part1.D11_PWM/MOSI, R1.Pin_0, U10.T2
  N5: Part1.D12/MISO, R1.Pin_1, R2.Pin_1, R3.Pin_1, R4.Pin_1, R5.Pin_1, R6.Pin_1, R7.Pin_1, R8.Pin_1, R9.Pin_1
  N6: Part1.D13/SCK, J2.pin2, LED1.cathode
  N7: Part1.GND, J2.pin1, LED1.anode
  N8: Part1.D3_PWM, R9.Pin_0, U4.T2
  N9: Part1.D4, R8.Pin_0, U3.T2
  N10: Part1.D5_PWM, R7.Pin_0, U7.T2
  N11: Part1.D6_PWM, R6.Pin_0, U2.T2
  N12: Part1.D7, R5.Pin_0, U6.T2
