# Fritzing sketch id4162_SIMPLE_LED_LIGHT (saved by Fritzing 0.6.4b)
breadboards: 1

parts:
  R1 = Resistor [tolerance=±5% resistance=220 package=THT]
  VCC1 = Battery
  LED1 = LED - 5mm [color="Red (633nm)" package="5 mm [THT]"]

nets:
  N1: R1.Pin_0, VCC1.+
  N2: R1.Pin_1, LED1.anode
  N3: VCC1.-, LED1.cathode

notes:
  FROM PURNA
