# Fritzing sketch id4162_Termometro_con_LED_RGB_0 (saved by Fritzing 0.9.1b)
breadboards: 1

parts:
  Parte1 = Arduino Uno (Rev3)
  T1 = LM35 Temperature Sensor [package="TO92 [THT]"]
  R1 = Resistor [tolerance=±5% resistance=330 package=THT]
  R2 = Resistor [tolerance=±5% resistance=330 package=THT]
  R3 = Resistor [tolerance=±5% resistance=330 package=THT]  # not connected
  LED1 = RGB LED - (4 legs) [package="5 mm [THT]"]

nets:
  N1: Parte1.A0, T1.Vout
  N2: Parte1.D5_PWM, R1.Pin_1
  N3: Parte1.D6_PWM, R2.Pin_1
  N4: Parte1.5V, T1.+Vs
  GND: Parte1.GND, T1.GND, LED1.common_anode
  N5: R1.Pin_0, LED1.blue_cathode
  N6: R2.Pin_0, LED1.red_cathode
