# Fritzing sketch id4163_Untitled_Sketch_2_0 (saved by Fritzing 0.9.3b)
breadboards: 1

parts:
  Part1 = Arduino Uno (Rev3)
  J1 = Piezo Speaker
  U1 = TMP36 [package=to-92]

nets:
  N1: Part1.A0, U1.VOUT
  N2: Part1.D9_PWM, J1.pin1
  GND: Part1.GND, J1.pin2, U1.GND
  5V: Part1.5V, U1.VCC
