# Fritzing sketch id4164_ServoThermo1_0 (saved by Fritzing 0.9.3b)
breadboards: 1

parts:
  Part1 = Arduino Nano (Rev3.0)
  R1 = Resistor [tolerance=±5% resistance=1k package="0402 [SMD]"]
  R2 = Temperature Sensor (Thermistor) [thermistor_type=NTC package=THT]
  M1 = Dagu DGServo 9g (End View) [part_number=RS001B]

nets:
  GND: Part1.GND, R1.Pin_0, M1.gnd
  5V: Part1.5V, R2.pin_0, M1.vcc
  N1: Part1.A4, M1.pulse
  N2: Part1.A0, R1.Pin_1, R2.pin_1
