# Fritzing sketch id4166_Node_RFM12b_STM32_release_0 (saved by Fritzing 0.7.12b)
breadboards: 1

parts:
  DC_Power1 = DC Power [voltage=3.3]
  J3_Debug = female pin header, 3 pins [form="♀ (female)"]
  J1_Power = female pin header, 3 pins [form="♀ (female)"]
  J2_SWD = female pin header, 3 pins [form="♀ (female)" part_number=SWD]
  Uart3r = female pin header, 3 pins [form="♀ (female)" part_number="Uart 3 Remap PD8 PD9"]
  Wake = female pin header, 2 pins [form="♀ (female)" part_number=WakeUp]
  R1 = Resistor [tolerance=±5% resistance=2.2k part_number=2.2K package="0603 [SMD]"]
  R2 = Resistor [tolerance=±5% resistance=1k part_number=1K package="0603 [SMD]"]
  C1 = Ceramic Capacitor [capacitance=100nF part_number=100nF package="0603 [SMD, multilayer]"]
  C2 = Ceramic Capacitor [capacitance=10µF part_number="10u VDD3" package="0603 [SMD, multilayer]"]
  C5 = Ceramic Capacitor [capacitance=10nF part_number=10n package="0603 [SMD, multilayer]"]
  C6 = Ceramic Capacitor [capacitance=1µF part_number=1u package="0603 [SMD, multilayer]"]
  R3 = Resistor [tolerance=±5% resistance=33k part_number=33K package="0603 [SMD]"]
  R4 = Resistor [tolerance=±5% resistance=10k part_number=10K package="0603 [SMD]"]
  R5 = Resistor [tolerance=±5% resistance=10k part_number=10K package="0603 [SMD]"]
  RFM12B1 = RFM12B Transceiver DIP Package
  RGB = female pin header, 4 pins [form="♀ (female)"]
  C3 = Ceramic Capacitor [capacitance=100nF part_number=100nF package="0603 [SMD, multilayer]"]
  C4 = Ceramic Capacitor [capacitance=100nF part_number=100nF package="0603 [SMD, multilayer]"]
  U1 = STM32F103 [part_number=STM32F100CB package=LQFP-48]
  Pad1 = Pad [width=0.5 height=2 connect=center]
  Pad2 = Pad [width=0.5 height=2 connect=center]
  Pad3 = Pad [width=0.5 height=0.5 connect=center]
  Pad4 = Pad [width=0.5 height=0.5 connect=center]
  Pad5 = Pad [width=0.5 height=0.5 connect=center]
  Pad6 = Pad [width=0.5 height=0.5 connect=center]
  Pad8 = Pad [width=0.5 height=0.5 connect=center]
  Pad7 = Pad [width=0.5 height=0.5 connect=center]
  Pad9 = Pad [width=0.5 height=0.5 connect=center]
  Pad10 = Pad [width=0.3 height=1 connect=center]
  Pad11 = Pad [width=0.3 height=1 connect=center]
  Pad12 = Pad [width=3 height=3 connect=center]
  Pad13 = Pad [width=2.5 height=2.5 connect=center]
  RGB1 = female pin header, 10 pins [form="♀ (female)"]
  RGB2 = female pin header, 10 pins [form="♀ (female)"]  # not connected
  R6 = Resistor [tolerance=±5% resistance=220 package="0603 [SMD]"]  # not connected
  R7 = Resistor [tolerance=±5% resistance=220 package="0603 [SMD]"]  # not connected
  R8 = Resistor [tolerance=±5% resistance=220 package="0603 [SMD]"]  # not connected
  R9 = Resistor [tolerance=±5% resistance=220 package="0603 [SMD]"]  # not connected
  R10 = Resistor [tolerance=±5% resistance=220 package="0603 [SMD]"]  # not connected
  R11 = Resistor [tolerance=±5% resistance=220 package="0603 [SMD]"]  # not connected
  R12 = Resistor [tolerance=±5% resistance=220 package="0603 [SMD]"]  # not connected
  R13 = Resistor [tolerance=±5% resistance=220 package="0603 [SMD]"]  # not connected
  R14 = Resistor [tolerance=±5% resistance=220 package="0603 [SMD]"]  # not connected
  R15 = Resistor [tolerance=±5% resistance=220 package="0603 [SMD]"]  # not connected
  R16 = Resistor [tolerance=±5% resistance=220 package="0603 [SMD]"]  # not connected
  R17 = Resistor [tolerance=±5% resistance=220 package="0603 [SMD]"]  # not connected

nets:
  3.3V: DC_Power1.V+, J1_Power.pin3, Wake.pin2, C1.1, C2.0, C5.0, C6.0, R5.Pin_0, RFM12B1.VDD, C3.0, C4.0, U1.VBAT, U1.VDDA, U1.VDD_2, U1.VDD_3, Pad1.pad, Pad13.pad, RGB1.pin1
  GND: DC_Power1.GND, J3_Debug.pin1, J1_Power.pin1, J2_SWD.pin1, Uart3r.pin1, R1.Pin_1, C2.1, C5.1, C6.1, R3.Pin_1, R4.Pin_1, RFM12B1.GND, RGB.pin1, C3.1, C4.1, U1.VSSA, U1.VSS_1, U1.VSS_2, U1.VSS_3, Pad2.pad, Pad12.pad, RGB1.pin10
  N1: J3_Debug.pin2, U1.PA10
  N2: J3_Debug.pin3, U1.PA9
  N3: J2_SWD.pin2, U1.PA14
  N4: J2_SWD.pin3, U1.PA13
  N5: Uart3r.pin2, U1.PA2
  N6: Uart3r.pin3, U1.PA3
  N7: Wake.pin1, R1.Pin_0, R2.Pin_0, C1.0
  N8: R2.Pin_1, U1.PA0-WKUP
  N9: R3.Pin_0, U1.PB2
  N10: R4.Pin_0, U1.BOOT0
  N11: R5.Pin_1, U1.NRST
  N12: RFM12B1.SDI, U1.PA7
  N13: RFM12B1.nSEL, U1.PA4
  N14: RFM12B1.nIRQ, U1.PA1
  N15: RFM12B1.SDO, U1.PA6
  N16: RFM12B1.SCK, U1.PA5
  N17: RGB.pin2, U1.PB11
  N18: RGB.pin3, U1.PB3
  N19: RGB.pin4, U1.PB4
  N20: U1.PB0, Pad3.pad
  N21: U1.PB1, Pad4.pad
  N22: U1.PB12, Pad9.pad
  N23: U1.PB13, Pad6.pad
  N24: U1.PB14, Pad7.pad
  N25: U1.PB15, Pad8.pad
  N26: U1.PA8, Pad5.pad
  N27: U1.PA11, Pad10.pad
  N28: U1.PA12, Pad11.pad
  N29: U1.PA15, RGB1.pin7
  N30: U1.PB5, RGB1.pin6
  N31: U1.PB6, RGB1.pin5
  N32: U1.PB7, RGB1.pin4
  N33: U1.PB8, RGB1.pin3
  N34: U1.PB9, RGB1.pin2

notes:
  Hier komt een Schakelaar
  C1
  R1
  R2
  F100CB
  R3
  R4
  R5
  Gnd
  R
  G
  B
  3.3v
  Sig
  Tx
  Rx
  C3
  C4
  VCC
  GND
  Vcc
  PB9
  PB8
  PB7
  PB6
  PB5
  PA15
  25-05-2013 RK01
  RFM12b Node V1
  Think_Rf V1
