# Fritzing sketch id4169_ccgame_0 (saved by Fritzing 0.9.3b)

parts:
  R1 = Resistor [tolerance=±5% resistance=750 package=THT]
  LED1 = LED - 5mm [color="Red (633nm)" package="5 mm [THT]"]
  R2 = Resistor [tolerance=±5% resistance=750 package=THT]
  LED2 = LED - 5mm [color="Red (633nm)" package="5 mm [THT]"]
  R3 = Resistor [tolerance=±5% resistance=750 package=THT]
  LED3 = LED - 5mm [color="Red (633nm)" package="5 mm [THT]"]
  R4 = Resistor [tolerance=±5% resistance=750 package=THT]
  LED4 = LED - 5mm [color="Red (633nm)" package="5 mm [THT]"]
  R5 = Resistor [tolerance=±5% resistance=750 package=THT]
  LED5 = LED - 5mm [color="Red (633nm)" package="5 mm [THT]"]
  R6 = Resistor [tolerance=±5% resistance=750 package=THT]
  LED6 = LED - 5mm [color="Red (633nm)" package="5 mm [THT]"]
  R7 = Resistor [tolerance=±5% resistance=750 package=THT]
  LED7 = LED - 5mm [color="Red (633nm)" package="5 mm [THT]"]
  R8 = Resistor [tolerance=±5% resistance=750 package=THT]
  LED8 = LED - 5mm [color="Red (633nm)" package="5 mm [THT]"]
  R9 = Resistor [tolerance=±5% resistance=750 package=THT]
  LED9 = LED - 5mm [color="Red (633nm)" package="5 mm [THT]"]
  LED10 = LED - 5mm [color="Blue (505nm)" package="5 mm [THT]"]
  R10 = Resistor [tolerance=±5% resistance=750 package=THT]
  R11 = Resistor [tolerance=±5% resistance=750 package=THT]
  LED11 = LED - 5mm [color="Blue (505nm)" package="5 mm [THT]"]
  R12 = Resistor [tolerance=±5% resistance=750 package=THT]
  LED12 = LED - 5mm [color="Blue (505nm)" package="5 mm [THT]"]
  R13 = Resistor [tolerance=±5% resistance=750 package=THT]
  LED13 = LED - 5mm [color="Blue (505nm)" package="5 mm [THT]"]
  R14 = Resistor [tolerance=±5% resistance=750 package=THT]
  LED14 = LED - 5mm [color="Blue (505nm)" package="5 mm [THT]"]
  R15 = Resistor [tolerance=±5% resistance=750 package=THT]
  LED15 = LED - 5mm [color="Blue (505nm)" package="5 mm [THT]"]
  R16 = Resistor [tolerance=±5% resistance=750 package=THT]
  LED16 = LED - 5mm [color="Blue (505nm)" package="5 mm [THT]"]
  R17 = Resistor [tolerance=±5% resistance=750 package=THT]
  LED17 = LED - 5mm [color="Blue (505nm)" package="5 mm [THT]"]
  R18 = Resistor [tolerance=±5% resistance=750 package=THT]
  LED18 = LED - 5mm [color="Blue (505nm)" package="5 mm [THT]"]
  S1 = Pushbutton [package=THT]
  S2 = Pushbutton [package=THT]
  R19 = Resistor [tolerance=±5% resistance=750 package=THT]
  R20 = Resistor [tolerance=±5% resistance=750 package=THT]
  S3 = Pushbutton [package=THT]
  S4 = Pushbutton [package=THT]
  R21 = Resistor [tolerance=±5% resistance=750 package=THT]
  R22 = Resistor [tolerance=±5% resistance=750 package=THT]
  S5 = Pushbutton [package=THT]
  S6 = Pushbutton [package=THT]
  R23 = Resistor [tolerance=±5% resistance=750 package=THT]
  R24 = Resistor [tolerance=±5% resistance=750 package=THT]
  S7 = Pushbutton [package=THT]
  S8 = Pushbutton [package=THT]
  R25 = Resistor [tolerance=±5% resistance=750 package=THT]
  R26 = Resistor [tolerance=±5% resistance=750 package=THT]
  S9 = Pushbutton [package=THT]
  S10 = Pushbutton [package=THT]
  R27 = Resistor [tolerance=±5% resistance=750 package=THT]
  R28 = Resistor [tolerance=±5% resistance=750 package=THT]
  S11 = Pushbutton [package=THT]
  S12 = Pushbutton [package=THT]
  R29 = Resistor [tolerance=±5% resistance=750 package=THT]
  R30 = Resistor [tolerance=±5% resistance=750 package=THT]
  S13 = Pushbutton [package=THT]
  S14 = Pushbutton [package=THT]
  R31 = Resistor [tolerance=±5% resistance=750 package=THT]
  R32 = Resistor [tolerance=±5% resistance=750 package=THT]
  S15 = Pushbutton [package=THT]
  S16 = Pushbutton [package=THT]
  R33 = Resistor [tolerance=±5% resistance=750 package=THT]
  R34 = Resistor [tolerance=±5% resistance=750 package=THT]
  パーツ1 = Arduino Mega 2560 (Rev3)
  S17 = Pushbutton [package=THT]
  S18 = Pushbutton [package=THT]
  R35 = Resistor [tolerance=±5% resistance=750 package=THT]
  R36 = Resistor [tolerance=±5% resistance=750 package=THT]
  R37 = Resistor [tolerance=±5% resistance=750 package=THT]
  R38 = Resistor [tolerance=±5% resistance=750 package=THT]
  LED19 = LED - 5mm [color="Red (633nm)" package="5 mm [THT]"]
  LED20 = LED - 5mm [color="Blue (505nm)" package="5 mm [THT]"]

nets:
  N1: R1.Pin_0, LED1.cathode
  N2: R1.Pin_1, R2.Pin_1, R3.Pin_1, R4.Pin_1, R5.Pin_0, R6.Pin_0, R7.Pin_0, R8.Pin_0, R9.Pin_0, R10.Pin_1, R11.Pin_1, R12.Pin_1, R13.Pin_1, R14.Pin_1, R15.Pin_1, R16.Pin_1, R17.Pin_1, R18.Pin_1, R19.Pin_1, R20.Pin_1, R21.Pin_1, R22.Pin_1, R23.Pin_1, R24.Pin_1, R25.Pin_1, R26.Pin_1, R27.Pin_0, R28.Pin_0, R29.Pin_0, R30.Pin_0, R31.Pin_0, R32.Pin_0, R33.Pin_0, R34.Pin_0, パーツ1.GND, R35.Pin_0, R36.Pin_0
  N3: LED1.anode, パーツ1.D22
  N4: R2.Pin_0, LED2.cathode
  N5: LED2.anode, パーツ1.D26
  N6: R3.Pin_0, LED3.cathode
  N7: LED3.anode, パーツ1.D30
  N8: R4.Pin_0, LED4.cathode
  N9: LED4.anode, パーツ1.D34
  N10: R5.Pin_1, LED5.cathode
  N11: LED5.anode, パーツ1.D38
  N12: R6.Pin_1, LED6.cathode
  N13: LED6.anode, パーツ1.D42
  N14: R7.Pin_1, LED7.cathode
  N15: LED7.anode, パーツ1.D46
  N16: R8.Pin_1, LED8.cathode
  N17: LED8.anode, パーツ1.D50
  N18: R9.Pin_1, LED9.cathode
  N19: LED9.anode, パーツ1.A0
  N20: LED10.cathode, R10.Pin_0
  N21: LED10.anode, パーツ1.D23
  N22: R11.Pin_0, LED11.cathode
  N23: LED11.anode, パーツ1.D27
  N24: R12.Pin_0, LED12.cathode
  N25: LED12.anode, パーツ1.D31
  N26: R13.Pin_0, LED13.cathode
  N27: LED13.anode, パーツ1.D35
  N28: R14.Pin_0, LED14.cathode
  N29: LED14.anode, パーツ1.D39
  N30: R15.Pin_0, LED15.cathode
  N31: LED15.anode, パーツ1.D43
  N32: R16.Pin_0, LED16.cathode
  N33: LED16.anode, パーツ1.D47
  N34: R17.Pin_0, LED17.cathode
  N35: LED17.anode, パーツ1.D51
  N36: R18.Pin_0, LED18.cathode
  N37: LED18.anode, パーツ1.A1
  N38: S1.leg0, S2.leg0, S3.leg0, S4.leg0, S5.leg0, S6.leg0, S7.leg0, S8.leg0, S9.leg1, S10.leg1, S11.leg1, S12.leg1, S13.leg1, S14.leg1, S15.leg1, S16.leg1, パーツ1.IOREF, S17.leg1, S18.leg1
  N39: S1.leg1, R19.Pin_0, パーツ1.D24
  N40: S2.leg1, R20.Pin_0, パーツ1.D25
  N41: S3.leg1, R22.Pin_0, パーツ1.D29
  N42: S4.leg1, R21.Pin_0, パーツ1.D28
  N43: S5.leg1, R24.Pin_0, パーツ1.D33
  N44: S6.leg1, R23.Pin_0, パーツ1.D32
  N45: S7.leg1, R26.Pin_0, パーツ1.D37
  N46: S8.leg1, R25.Pin_0, パーツ1.D36
  N47: S9.leg0, R28.Pin_1
  N48: S10.leg0, R27.Pin_1, パーツ1.D41
  N49: S11.leg0, R30.Pin_1
  N50: S12.leg0, R29.Pin_1
  N51: S13.leg0, R32.Pin_1
  N52: S14.leg0, R31.Pin_1
  N53: S15.leg0, R34.Pin_1
  N54: S16.leg0, R33.Pin_1, パーツ1.D53
  N55: パーツ1.A2, S18.leg0, R36.Pin_1
  N56: パーツ1.A3, S17.leg0, R35.Pin_1
  N57: パーツ1.A5, LED19.anode
  N58: パーツ1.A6, LED20.anode
  N59: R37.Pin_0, LED20.cathode
  N60: R37.Pin_1, R38.Pin_0
  N61: R38.Pin_1, LED19.cathode
