# Fritzing sketch id416_Untitled_Sketch_2_0 (saved by Fritzing 0.9.3b)
circuit board: 8.39763cm x 6.3953cm
breadboards: 2

parts:
  R1 = Resistor [tolerance=±5% resistance=10k package=THT]
  R2 = Resistor [tolerance=±5% resistance=10k package=THT]
  U1 = 74HC595 [package="DIP16 [THT]"]
  LED1 = LED - 5mm [color="Blue (505nm)" package="5 mm [THT]"]
  LED2 = LED - 5mm [color="Blue (505nm)" package="5 mm [THT]"]
  LED3 = LED - 5mm [color="Blue (505nm)" package="5 mm [THT]"]
  LED4 = LED - 5mm [color="Blue (505nm)" package="5 mm [THT]"]
  LED5 = LED - 5mm [color="Blue (505nm)" package="5 mm [THT]"]
  LED6 = LED - 5mm [color="Blue (505nm)" package="5 mm [THT]"]
  LED7 = LED - 5mm [color="Blue (505nm)" package="5 mm [THT]"]
  LED8 = LED - 5mm [color="Blue (505nm)" package="5 mm [THT]"]
  LED9 = LED - 5mm [color="Blue (505nm)" package="5 mm [THT]"]
  LED10 = LED - 5mm [color="Blue (505nm)" package="5 mm [THT]"]
  LED11 = LED - 5mm [color="Blue (505nm)" package="5 mm [THT]"]
  R3 = Resistor [tolerance=±5% resistance=470 package=THT]
  R4 = Resistor [tolerance=±5% resistance=470 package=THT]
  R5 = Resistor [tolerance=±5% resistance=470 package=THT]
  R6 = Resistor [tolerance=±5% resistance=470 package=THT]
  R7 = Resistor [tolerance=±5% resistance=470 package=THT]
  R8 = Resistor [tolerance=±5% resistance=470 package=THT]
  R9 = Resistor [tolerance=±5% resistance=470 package=THT]
  R10 = Resistor [tolerance=±5% resistance=470 package=THT]
  R11 = Resistor [tolerance=±5% resistance=470 package=THT]
  R12 = Resistor [tolerance=±5% resistance=470 package=THT]
  R13 = Resistor [tolerance=±5% resistance=470 package=THT]
  J1 = female pin header, 10 pins [form="♀ (female)"]
  U2 = 74HC595 [package="DIP16 [THT]"]
  S1 = Pushbutton [package="[THT]"]
  S2 = Pushbutton [package="[THT]"]

nets:
  N1: R1.Pin_0, R2.Pin_0, U1.Q7', U1.OE, R3.Pin_0, R4.Pin_0, R5.Pin_0, R6.Pin_0, R7.Pin_0, R8.Pin_0, R9.Pin_0, R10.Pin_0, R11.Pin_0, R12.Pin_0, R13.Pin_0, J1.pin1, U2.GND, U2.OE
  N2: R1.Pin_1, J1.pin9, S2.Pin_1, S2.Pin_2
  N3: R2.Pin_1, J1.pin8, S1.Pin_1, S1.Pin_2
  N4: U1.Q1, LED7.anode
  N5: U1.Q2, LED6.anode
  N6: U1.Q3, LED8.anode
  N7: U1.Q4, LED10.anode
  N8: U1.Q5, LED11.anode
  VCC: U1.MR, U1.VCC, J1.pin10, U2.MR, U2.VCC, S1.Pin_3, S1.Pin_4, S2.Pin_3, S2.Pin_4
  N9: U1.SH_CP, J1.pin7
  N10: U1.ST_CP, J1.pin6
  N11: U1.DS, J1.pin5
  N12: U1.Q0, LED5.anode
  N13: LED1.cathode, R4.Pin_1
  N14: LED1.anode, U2.Q1
  N15: LED2.cathode, R5.Pin_1
  N16: LED2.anode, U2.Q2
  N17: LED3.cathode, R6.Pin_1
  N18: LED3.anode, U2.Q3
  N19: LED4.cathode, R7.Pin_1
  N20: LED4.anode, U2.Q4
  N21: LED5.cathode, R8.Pin_1
  N22: LED6.cathode, R10.Pin_1
  N23: LED7.cathode, R9.Pin_1
  N24: LED8.cathode, R11.Pin_1
  N25: LED9.cathode, R3.Pin_1
  N26: LED9.anode, U2.Q0
  N27: LED10.cathode, R12.Pin_1
  N28: LED11.cathode, R13.Pin_1
  N29: J1.pin2, U2.DS
  N30: J1.pin3, U2.ST_CP
  N31: J1.pin4, U2.SH_CP
