# Fritzing sketch id4170_diagarama_del_proyecto_de_tics_2_0 (saved by Fritzing 0.9.3b)
breadboards: 1

parts:
  Componente1 = Arduino Uno (Rev3)
  BAT1 = BC9VPC [package=bc9vpc]  # not connected
  hc-sr1 = hc-sr04
  IC1 = L293D [package=THT]
  Componente2 = Bluetooth HC-05 Macho
  M2 = DC Motor
  M3 = DC Motor
  LED1 = LED - 5mm [color="Red (633nm)" package="5 mm [THT]"]

nets:
  N1: Componente1.D9_PWM, IC1.In_2
  N2: Componente1.D10_PWM/SS, IC1.In_1
  N3: Componente1.D13/SCK, LED1.anode
  N4: Componente1.GND, LED1.cathode
  N5: Componente1.D0/RX, Componente2.TXD
  N6: Componente1.D1/TX, Componente2.RXD
  N7: Componente1.D2, hc-sr1.Echo
  N8: Componente1.D3_PWM, hc-sr1.Trig
  N9: Componente1.D5_PWM, IC1.In_3
  N10: Componente1.D6_PWM, IC1.In_4
  N11: Componente1.VIN, IC1.+Vmotor
  N12: IC1.Out_1_(_Controlled_by_Enable_1_), M2.pin_1
  N13: IC1.Out_2_(_Controlled_by_Enable_1_), M2.pin_2
  N14: IC1.Out_3_(_Controlled_by_Enable_2_), M3.pin_1
  N15: IC1.Out_4_(_Controlled_by_Enable_2_), M3.pin_2
