# Fritzing sketch id4171_TicTacToe_0 (saved by Fritzing 0.7.12b)
breadboards: 1

parts:
  Arduino1 = Arduino
  S1 = Toggle Switch [package=THT]
  R4 = Resistor [tolerance=±5% resistance=10k package=THT]
  S2 = Toggle Switch [package=THT]
  R5 = Resistor [tolerance=±5% resistance=1M package=THT]
  S3 = Toggle Switch [package=THT]
  R6 = Resistor [tolerance=±5% resistance=10k package=THT]
  R8 = Resistor [tolerance=±5% resistance=1M package=THT]
  S5 = Toggle Switch [package=THT]
  S6 = Toggle Switch [package=THT]
  R9 = Resistor [tolerance=±5% resistance=10k package=THT]
  S4 = Toggle Switch [package=THT]
  R10 = Resistor [tolerance=±5% resistance=10k package=THT]
  R11 = Resistor [tolerance=±5% resistance=1M package=THT]
  S8 = Toggle Switch [package=THT]
  S9 = Toggle Switch [package=THT]
  R12 = Resistor [tolerance=±5% resistance=10k package=THT]
  S7 = Toggle Switch [package=THT]
  R7 = Resistor [tolerance=±5% resistance=10k package=THT]

nets:
  N1: Arduino1.+5V, S1.L2, S2.L2, S3.L2, S5.L2, S6.L2, S4.L2, S8.L2, S9.L2, S7.L2
  N2: Arduino1.GND, R4.Pin_0, R10.Pin_0, R7.Pin_0
  N3: Arduino1.A0, S1.COM, R4.Pin_1, R5.Pin_0
  N4: Arduino1.A1, R8.Pin_0, S4.COM, R7.Pin_1
  N5: Arduino1.A2, R10.Pin_1, R11.Pin_0, S7.COM
  N6: S2.COM, R5.Pin_1, R6.Pin_0
  N7: S3.COM, R6.Pin_1
  N8: R8.Pin_1, S5.COM, R9.Pin_0
  N9: S6.COM, R9.Pin_1
  N10: R11.Pin_1, S8.COM, R12.Pin_0
  N11: S9.COM, R12.Pin_1
