# Fritzing sketch id4173_Diagrama_0 (saved by Fritzing 0.9.2b)
circuit board: 5.15314cm x 5.72404cm
breadboards: 1

parts:
  Parte1 = Arduino Mega 2560 (Rev3)
  AM1 = AM2302_Humidity_and_Temperature_Sensor
  R1 = Resistor [tolerance=±5% resistance=10 package=THT]
  U1 = MLX90614_1
  R2 = Resistor [tolerance=±5% resistance=10 package=THT]
  R3 = Resistor [tolerance=±5% resistance=10 package=THT]
  BREAKOUT2 = ThermocoupleAdaptor
  Parte2 = Memoire 1.0 - SD card log shield

nets:
  N1: Parte1.D21/SCL, U1.connector0, R2.Pin_0
  N2: Parte1.D20/SDA, U1.connector1, R3.Pin_0
  N3: Parte1.D13_PWM, Parte2.DIG_13
  N4: Parte1.D12_PWM, Parte2.DIG_12
  N5: Parte1.D10_PWM, Parte2.DIG_10
  5V: Parte1.5V, AM1.connector1, R1.Pin_1, U1.connector2, R2.Pin_1, R3.Pin_1, BREAKOUT2.connector2, Parte2.+5V
  GND: Parte1.GND, AM1.connector3, U1.connector3, BREAKOUT2.connector1, Parte2.GND
  N6: Parte1.D2_PWM, AM1.connector2, R1.Pin_0
  N7: Parte1.D44, Parte2.DIG_11
  N8: Parte1.D49, BREAKOUT2.connector4
  N9: Parte1.D50, BREAKOUT2.connector6
  N10: Parte1.D51, BREAKOUT2.connector7
  N11: Parte1.D52, BREAKOUT2.connector5
