# Fritzing sketch id4175_Tilduino_V1.1_II_0 (saved by Fritzing 0.6.3b)
breadboards: 1

parts:
  U1 = Voltage Regulator - 5V [package="TO220 [THT]"]
  J1 = Screw terminal - 2 pins [package=THT]
  C6 = Ceramic Capacitor [capacitance=100nF package="100 mil [THT, multilayer]"]
  C5 = Electrolytic Capacitor [capacitance=1µF package="100 mil [THT, electrolytic]"]
  C8 = Electrolytic Capacitor [capacitance=1µF package="100 mil [THT, electrolytic]"]
  D2 = Rectifier Diode [part_number=1N4001 package="300 mil [THT]"]
  LED1 = LED - 5mm [color="Green (570nm)" package="5 mm [THT]"]
  C2 = Ceramic Capacitor [capacitance=100nF package="100 mil [THT, multilayer]"]
  C4 = Ceramic Capacitor [capacitance=100nF package="100 mil [THT, multilayer]"]
  MHZ16 = Crystal [frequency="16 Mhz" package=THT]
  SCK = LED - 5mm [color="Green (570nm)" package="5 mm [THT]"]
  C3 = Ceramic Capacitor [capacitance=100nF package="100 mil [THT, multilayer]"]
  C7 = Ceramic Capacitor [capacitance=100nF package="100 mil [THT, multilayer]"]
  D1 = Resistor [tolerance=±5% resistance=220 package=THT]
  U4 = atmega168 [package="DIP28 [THT]"]
  C1 = Ceramic Capacitor [capacitance=100nF package="100 mil [THT, multilayer]"]
  R2 = Resistor [tolerance=±5% resistance=1.5k package=THT]
  R3 = Resistor [tolerance=±5% resistance=220 package=THT]
  R1 = Resistor [tolerance=±5% resistance=220 package=THT]
  S1 = Pushbutton [package=THT]

nets:
  N1: U1.input_voltage, C6.0, C5.+, D2.cathode, D1.Pin_0
  N2: U1.GND, J1.pin1, C6.1, C5.-, C8.-, LED1.cathode, C2.0, C4.1, SCK.cathode, C3.0, C7.0, U4.Pin_8, U4.Pin_22, S1.leg0
  N3: U1.output_voltage, C8.+, D2.anode, C2.1, C7.1, U4.Pin_7, U4.Pin_20, R2.Pin_0, R1.Pin_0
  N4: LED1.anode, R1.Pin_1
  N5: C4.0, MHZ16.pin_1, U4.Pin_10
  N6: MHZ16.pin_0, C3.1, U4.Pin_9
  N7: SCK.anode, R3.Pin_1
  N8: U4.Pin_1, C1.1, R2.Pin_1, S1.leg1
  N9: U4.Pin_19, R3.Pin_0

notes:
  -
  ------------
  ---
  Tilduino V1.1
  ATMEGA 168P/328P
  1
  2
  3
  4
  5
  6
  B1
  MOSI
  MISO
  SCK
  GND
  LED1
  Power
  www.tilduino.de
  LED2
  VCC
  -----
  J2
  RST
  B2
  Q1
  S2
  |
  SSP
