# Fritzing sketch id4176_Tilt_Controlled_Servo_0 (saved by Fritzing 0.8.3b)
circuit board: 16.9333cm x 5.64444cm
breadboards: 1

parts:
  Part1 = Arduino Uno (Rev3)
  S1 = Tilt Switch [package=THT]
  10k_Resistor = Resistor [tolerance=±5% resistance=10k package=THT]
  J1 = Basic Servo

nets:
  GND: Part1.GND, 10k_Resistor.Pin_1, J1.gnd
  N1: Part1.D9_PWM, J1.pulse
  N2: Part1.D2, S1.Pin_2, 10k_Resistor.Pin_0
  5V: Part1.5V, S1.Pin_1, J1.vcc

notes:
  Tilt Controlled Servo
