# Fritzing sketch id4177_Untitled_Sketch_3_0 (saved by Fritzing 0.9.0b)
breadboards: 1

parts:
  S1 = Tilt Switch [package=THT]
  S2 = Tilt Switch [package=THT]
  Part1 = Arduino Uno (Rev3)
  LED1 = LED - 5mm [color="Red (633nm)" package="5 mm [THT]"]
  LED2 = LED - 5mm [color="Red (633nm)" package="5 mm [THT]"]
  R1 = Resistor [tolerance=±5% resistance=10k package=THT]
  R2 = Resistor [tolerance=±5% resistance=10k package=THT]
  R3 = Resistor [tolerance=±5% resistance=220 package=THT]
  R4 = Resistor [tolerance=±5% resistance=220 package=THT]

nets:
  N1: S1.Pin_1, R1.Pin_1
  N2: S1.Pin_2, S2.Pin_1, Part1.5V
  N3: S2.Pin_2, R2.Pin_1
  N4: Part1.A0, R2.Pin_0
  N5: Part1.A1, R1.Pin_0
  N6: Part1.D12/MISO, LED2.anode
  N7: Part1.D13/SCK, LED1.cathode
  N8: Part1.GND, R3.Pin_1, R4.Pin_1
  N9: LED1.anode, R3.Pin_0
  N10: LED2.cathode, R4.Pin_0
