# Fritzing sketch id4178_GeekSpot_TiltSwitch_0 (saved by Fritzing 0.8.5b)
breadboards: 1

parts:
  Part1 = Arduino Uno (Rev3)
  LED2 = LED - 5mm [color="Red (633nm)" package="5 mm [THT]"]
  LED3 = LED - 5mm [color="Red (633nm)" package="5 mm [THT]"]
  R1 = Resistor [tolerance=±5% resistance=220 package=THT]
  S1 = Tilt Switch [package=THT]

nets:
  N1: Part1.D12/MISO, LED3.anode
  N2: Part1.D13/SCK, LED2.anode
  N3: Part1.GND, LED2.cathode, LED3.cathode, S1.Pin_1
  N4: Part1.D2, R1.Pin_0, S1.Pin_2
  N5: Part1.5V, R1.Pin_1
