# Fritzing sketch id417_Binuhr_Fritzing_0 (saved by Fritzing 0.8.7b)
circuit board: 7.89746cm x 5.74555cm
breadboards: 2

parts:
  sec1 = LED - 5mm [color="Red (633nm)" package="5 mm [THT]"]
  sec2 = LED - 5mm [color="Red (633nm)" package="5 mm [THT]"]
  sec4 = LED - 5mm [color="Red (633nm)" package="5 mm [THT]"]
  sec8 = LED - 5mm [color="Red (633nm)" package="5 mm [THT]"]
  sec16 = LED - 5mm [color="Red (633nm)" package="5 mm [THT]"]
  sec32 = LED - 5mm [color="Red (633nm)" package="5 mm [THT]"]
  min1 = LED - 5mm [color="Yellow (595nm)" package="5 mm [THT]"]
  min2 = LED - 5mm [color="Yellow (595nm)" package="5 mm [THT]"]
  min4 = LED - 5mm [color="Yellow (595nm)" package="5 mm [THT]"]
  min8 = LED - 5mm [color="Yellow (595nm)" package="5 mm [THT]"]
  min16 = LED - 5mm [color="Yellow (595nm)" package="5 mm [THT]"]
  min32 = LED - 5mm [color="Yellow (595nm)" package="5 mm [THT]"]
  U2 = PCF8574 [package="DIP16 [THT]"]
  U3 = PCF8574 [package="DIP16 [THT]"]
  U1 = PCF8574 [package="DIP16 [THT]"]
  hor8 = LED - 5mm [color="Green (570nm)" package="5 mm [THT]"]
  hor4 = LED - 5mm [color="Green (570nm)" package="5 mm [THT]"]
  hor2 = LED - 5mm [color="Green (570nm)" package="5 mm [THT]"]
  hor1 = LED - 5mm [color="Green (570nm)" package="5 mm [THT]"]
  Bauteil1 = Arduino Uno (Rev3)
  R18 = Resistor [tolerance=±1% resistance=4.7k package=THT]
  R19 = Resistor [tolerance=±1% resistance=4.7k package=THT]
  SetH = Pushbutton [package="[THT]"]
  Res = Pushbutton [package="[THT]"]
  SetM = Pushbutton [package="[THT]"]

nets:
  GND: sec1.cathode, sec2.cathode, sec4.cathode, sec8.cathode, sec16.cathode, sec32.cathode, min1.cathode, min2.cathode, min4.cathode, min8.cathode, min16.cathode, min32.cathode, U2.A1, U2.A3, U2.GND, U3.A0, U3.A1, U3.A3, U3.GND, U1.A3, U1.GND, hor8.cathode, hor4.cathode, hor2.cathode, hor1.cathode, Bauteil1.GND, R18.Pin_0, R19.Pin_0, SetH.Pin_1, SetH.Pin_2, SetM.Pin_1, SetM.Pin_2
  N1: sec1.anode, U3.P0
  N2: sec2.anode, U3.P1
  N3: sec4.anode, U3.P2
  N4: sec8.anode, U3.P3
  N5: sec16.anode, U3.P4
  N6: sec32.anode, U3.P5
  N7: min1.anode, U2.P0
  N8: min2.anode, U2.P1
  N9: min4.anode, U2.P2
  N10: min8.anode, U2.P3
  N11: min16.anode, U2.P4
  N12: min32.anode, U2.P5
  VCC: U2.A0, U2.VCC, U3.VCC, U1.A0, U1.A1, U1.VCC, Bauteil1.5V
  N13: U2.SCL, U3.SCL, U1.SCL, Bauteil1.A5/SCL, R18.Pin_1
  N14: U2.SDA, U3.SDA, U1.SDA, Bauteil1.A4/SDA, R19.Pin_1
  N15: U1.P0, hor1.anode
  N16: U1.P1, hor2.anode
  N17: U1.P2, hor4.anode
  N18: U1.P3, hor8.anode
  N19: Bauteil1.D2, SetM.Pin_3, SetM.Pin_4
  N20: Bauteil1.D3_PWM, SetH.Pin_3, SetH.Pin_4
  N21: Bauteil1.D4, Res.Pin_3, Res.Pin_4
  N22: Bauteil1.RESET, Res.Pin_1, Res.Pin_2
