# Fritzing sketch id4180_TimeDelayLockbox_0 (saved by Fritzing 0.9.3b)
breadboards: 1

parts:
  Part1 = Arduino Nano (Rev3.0)  # not connected
  Grove1 = Grove 4 Digit Display
  S1 = Pushbutton [package="[SMD]"]
  S2 = Taiway 100-SP-X-T1 SPDT Miniature Toggle Switch [part_number=100-SP-X-T1-0-0-B1-M1 package=THT]
  RE_EC1 = EC11 [part_number=EC1110120201]
  Q1 = MOSFET-NCHANNEL [package=to220v]
  D1 = Rectifier Diode [part_number=1N4001 package="300 mil [THT]"]
  R1 = Resistor [tolerance=±5% resistance=10k package=THT]
  L1 = Solenoid
  VCC1 = Battery block 9V
  M1 = RioRand LM2596

nets:
  N1: Grove1.GND, S1.Pin_3, S1.Pin_4, S2.COM, RE_EC1.connector1, Q1.D, Q1.S, D1.anode, R1.Pin_1, L1.pin1, VCC1.-, M1.Pin_2, M1.Pin_4
  N2: S1.Pin_1, S1.Pin_2
  N3: Q1.G, R1.Pin_0
  N4: D1.cathode, L1.pin2, VCC1.+, M1.Pin_1

notes:
  12V Actually
  Step Down from 12V to 5V
