# Fritzing sketch id4181_Time_Lapsing_Rotor_0 (saved by Fritzing 0.7.12b)
breadboards: 1

parts:
  R1 = Rotary Potentiometer (Small) [maximum_resistance=100kΩ]
  Arduino1 = Arduino
  J1 = Basic Servo
  LED1 = LED - 5mm [color="Green (555nm)" package="5 mm [THT]"]
  LED2 = LED - 5mm [color="Red (633nm)" package="5 mm [THT]"]
  R2 = Resistor [tolerance=±5% resistance=1k package=THT]
  R4 = Resistor [tolerance=±5% resistance=1k package=THT]

nets:
  +5V: R1.leg1, Arduino1.+5V, J1.vcc
  N1: R1.wiper, Arduino1.A0
  GND: R1.leg2, Arduino1.GND, J1.gnd, R2.Pin_0, R4.Pin_0
  N2: Arduino1.D10, J1.pulse
  N3: Arduino1.D7, LED2.anode
  N4: Arduino1.D6, LED1.anode
  N5: LED1.cathode, R2.Pin_1
  N6: LED2.cathode, R4.Pin_1

notes:
  //Time Lapsing Rotory by D.C.R
  #include <Servo.h>
  Servo myservo; // create servo object to control a servo
  int potpin = 0; // analog pin used to connect the potentiometer
  int val; // variable to read the value from the analog pin
  int Green = 6;
  int Red = 7;
  void setup()
  {
  pinMode(Green, OUTPUT);
  pinMode(Red, OUTPUT);
  myservo.attach(9); // attaches the servo on pin 9 to the servo object
  // initialize serial communications at 9600 bps:
  Serial.begin(9600);
  digitalWrite(Green, LOW);
  digitalWrite(Red, LOW);
  }
  void loop()
  {
  val = analogRead(potpin); // reads the value of the potentiometer (value between 0 and 1023)
  val = map(val, 0, 1023, 179, 0); // scale it to use it with the servo (value between 0 and 180)
  myservo.write(val); // sets the servo position according to the scaled value
  if(val < 93) {
  digitalWrite(Green, HIGH);
  digitalWrite(Red, LOW);
  } else if(val > 96) {
  digitalWrite(Green, LOW);
  digitalWrite(Red, HIGH);
  } else {
  digitalWrite(Green, LOW);
  digitalWrite(Red, LOW);
  }
  // print the results to the serial monitor:
  Serial.print("knob = " );
  Serial.println(val);
  delay(15); // waits for the servo to get there
  }
