# Fritzing sketch id4182_timer_0 (saved by Fritzing 0.9.0b)
breadboards: 1

parts:
  LCD1 = LCD screen
  Part1 = Arduino Leonardo (Rev3b)
  S1 = Pushbutton [package="[THT]"]
  S2 = Pushbutton [package="[THT]"]
  S3 = Pushbutton [package="[THT]"]
  S4 = Pushbutton [package="[THT]"]
  R1 = Trimmer Potentiometer [maximum_resistance=10kΩ package=THT]
  R2 = Resistor [tolerance=±5% resistance=220 package=THT]
  R3 = Resistor [tolerance=±5% resistance=220 package=THT]
  R4 = Resistor [tolerance=±5% resistance=220 package=THT]
  R5 = Resistor [tolerance=±5% resistance=220 package=THT]
  LED1 = LED - 5mm [color="Yellow (595nm)" package="5 mm [THT]"]
  R6 = Resistor [tolerance=±5% resistance=220 package=THT]
  J1 = Piezo Speaker
  R7 = Resistor [tolerance=±5% resistance=220 package=THT]

nets:
  VSS: LCD1.VSS, LCD1.R/W, LCD1.LED-, Part1.GND, R1.leg2, R2.Pin_0, R3.Pin_0, R5.Pin_0, R6.Pin_0, J1.pin1
  VDD: LCD1.VDD, Part1.5V, S1.Pin_1, S1.Pin_2, S2.Pin_1, S2.Pin_2, S3.Pin_1, S3.Pin_2, S4.Pin_1, S4.Pin_2, R1.leg1
  N1: LCD1.V0, R1.wiper
  N2: LCD1.RS, Part1.D12/A11
  N3: LCD1.E, Part1.D11_PWM
  N4: LCD1.DB4, Part1.D9_PWM/A9
  N5: LCD1.DB5, Part1.D8/A8
  N6: LCD1.DB6, Part1.D7
  N7: LCD1.DB7, Part1.D6_PWM/A7
  N8: LCD1.LED+, Part1.D5_PWM
  N9: Part1.D1/TX, S1.Pin_3, S1.Pin_4, R2.Pin_1
  N10: Part1.D2/SDA, S2.Pin_3, S2.Pin_4, R5.Pin_1
  N11: Part1.D3_PWM/SCL, S3.Pin_3, S3.Pin_4, R4.Pin_1
  N12: Part1.D4/A6, S4.Pin_3, S4.Pin_4, R3.Pin_1
  N13: Part1.D10_PWM/A10, R7.Pin_0
  N14: Part1.D13_PWM, LED1.anode
  N15: LED1.cathode, R6.Pin_1
  N16: J1.pin2, R7.Pin_1

notes:
  down/up set/start
