# Fritzing sketch id4183_sketchtimer_0 (saved by Fritzing 0.9.3b)
breadboards: 1

parts:
  S1 = Pushbutton [package="[THT]"]
  Composant1 = Arduino Uno (Rev3)
  7_Segment_4_Digit_Display_SMA420564_http_//haneefputtur_com/7-segment-4-digit-led-display-sma420564-using-arduino_html = CLab [part_number="5461BS - 5462BS"]
  R1 = Resistor [tolerance=±5% resistance=220 package="0402 [SMD]"]
  R2 = Resistor [tolerance=±5% resistance=220 package="0402 [SMD]"]
  R4 = Resistor [tolerance=±5% resistance=220 package="0402 [SMD]"]
  S2 = Pushbutton [package="[THT]"]
  S3 = Pushbutton [package="[THT]"]
  R5 = Resistor [tolerance=±5% resistance=220 package="1206 [SMD]"]
  R6 = Resistor [tolerance=±5% resistance=220 package="1206 [SMD]"]
  R7 = Resistor [tolerance=±5% resistance=220 package="1206 [SMD]"]
  R3 = Resistor [tolerance=±5% resistance=220 package="0402 [SMD]"]
  R8 = Resistor [tolerance=±5% resistance=470 package=THT]

nets:
  N1: S1.Pin_1, S1.Pin_2, Composant1.A0, R5.Pin_0
  N2: S1.Pin_3, S1.Pin_4, Composant1.5V, S2.Pin_3, S2.Pin_4, S3.Pin_3, S3.Pin_4
  N3: Composant1.A1, S2.Pin_1, S2.Pin_2, R6.Pin_0
  N4: Composant1.A2, S3.Pin_1, S3.Pin_2, R7.Pin_0
  N5: Composant1.D8, 7_Segment_4_Digit_Display_SMA420564_http_//haneefputtur_com/7-segment-4-digit-led-display-sma420564-using-arduino_html.connector5
  N6: Composant1.D9_PWM, 7_Segment_4_Digit_Display_SMA420564_http_//haneefputtur_com/7-segment-4-digit-led-display-sma420564-using-arduino_html.connector3
  N7: Composant1.D10_PWM/SS, R1.Pin_0
  N8: Composant1.D11_PWM/MOSI, R4.Pin_1
  N9: Composant1.D12/MISO, R3.Pin_1
  N10: Composant1.D13/SCK, R2.Pin_1
  N11: Composant1.GND, R5.Pin_1, R6.Pin_1, R7.Pin_1
  N12: Composant1.D0/RX, R8.Pin_1
  N13: Composant1.D2, 7_Segment_4_Digit_Display_SMA420564_http_//haneefputtur_com/7-segment-4-digit-led-display-sma420564-using-arduino_html.connector11
  N14: Composant1.D3_PWM, 7_Segment_4_Digit_Display_SMA420564_http_//haneefputtur_com/7-segment-4-digit-led-display-sma420564-using-arduino_html.connector7
  N15: Composant1.D4, 7_Segment_4_Digit_Display_SMA420564_http_//haneefputtur_com/7-segment-4-digit-led-display-sma420564-using-arduino_html.connector4
  N16: Composant1.D5_PWM, 7_Segment_4_Digit_Display_SMA420564_http_//haneefputtur_com/7-segment-4-digit-led-display-sma420564-using-arduino_html.connector2
  N17: Composant1.D6_PWM, 7_Segment_4_Digit_Display_SMA420564_http_//haneefputtur_com/7-segment-4-digit-led-display-sma420564-using-arduino_html.connector1
  N18: Composant1.D7, 7_Segment_4_Digit_Display_SMA420564_http_//haneefputtur_com/7-segment-4-digit-led-display-sma420564-using-arduino_html.connector10
  N19: 7_Segment_4_Digit_Display_SMA420564_http_//haneefputtur_com/7-segment-4-digit-led-display-sma420564-using-arduino_html.connector6, R1.Pin_1
  N20: 7_Segment_4_Digit_Display_SMA420564_http_//haneefputtur_com/7-segment-4-digit-led-display-sma420564-using-arduino_html.connector8, R4.Pin_0
  N21: 7_Segment_4_Digit_Display_SMA420564_http_//haneefputtur_com/7-segment-4-digit-led-display-sma420564-using-arduino_html.connector9, R3.Pin_0
  N22: 7_Segment_4_Digit_Display_SMA420564_http_//haneefputtur_com/7-segment-4-digit-led-display-sma420564-using-arduino_html.connector12, R2.Pin_0

notes:
  Afficheur 7 segments - 4 chiffres
  Attention, l'afficheur utilise sur le proto est un SMA 420 564 et non pas la reference de Fritzing. La vue schematique n'est peut-être pas bonne mais la vue de la Platine d'essai en termes de branchements est OK
  Doc des branchements prise sur
  http://haneefputtur.com/7-segment-4-digit-led-display-sma420564-using-sarduino.html
  ----------------------------------------------------------------------------------------------------
  7 segments display - 4 digits.
  Be careful, the wires displayed are put in the correct layout for the SMA420564 7 segment display, not for the 5461BS (which is supposed to be the one used here). Not sure if the schematic view is good then.
  I got the informations for SMA420564 here :
  http://haneefputtur.com/7-segment-4-digit-led-display-sma420564-using-sarduino.html
  Ici, Brancher le Néopixel strip ou ring. Bien indiquer après coup le nombre de LED total dans le code Arduino.
  ----------------------------------------
  Here, plug a neopixel strip or a Neopixel Ring.
  Be sure that you put the exact number of LED in the Arduino code afterwards.
  Dans l'ordre : Bouton Start / Bouton Moins / Bouton Plus
  ----------
  From left to right : Button Start / Button - / Bouton +
