# Fritzing sketch id4184_Timer_0 (saved by Fritzing 0.9.3b)
breadboards: 1

parts:
  Composant1 = Arduino Uno (Rev3)
  7_Segment_4_Digit_Display1 = CLab [part_number=5461AS]
  R1 = Resistor [tolerance=±5% resistance=220 package=THT]
  R2 = Resistor [tolerance=±5% resistance=220 package=THT]
  R5 = Resistor [tolerance=±5% resistance=220 package=THT]
  R6 = Resistor [tolerance=±5% resistance=220 package=THT]
  Composant2 = adafruit [part_number=1586]
  S1 = Pushbutton [package="[THT]"]
  S2 = Pushbutton [package="[THT]"]
  S3 = Pushbutton [package="[THT]"]
  R7 = Resistor [tolerance=±5% resistance=220 package=THT]
  R8 = Resistor [tolerance=±5% resistance=220 package=THT]
  R9 = Resistor [tolerance=±5% resistance=220 package=THT]

nets:
  N1: Composant1.A0, 7_Segment_4_Digit_Display1.connector1
  N2: Composant1.A1, 7_Segment_4_Digit_Display1.connector2
  N3: Composant1.A2, 7_Segment_4_Digit_Display1.connector3
  N4: Composant1.A3, 7_Segment_4_Digit_Display1.connector4
  N5: Composant1.A4/SDA, 7_Segment_4_Digit_Display1.connector5
  N6: Composant1.A5/SCL, R5.Pin_0
  N7: Composant1.D8, 7_Segment_4_Digit_Display1.connector7
  N8: Composant1.D9_PWM, R6.Pin_0
  N9: Composant1.D10_PWM/SS, R2.Pin_0
  N10: Composant1.D11_PWM/MOSI, 7_Segment_4_Digit_Display1.connector10
  N11: Composant1.D12/MISO, 7_Segment_4_Digit_Display1.connector11
  N12: Composant1.D13/SCK, R1.Pin_0
  N13: Composant1.GND, Composant2.connector40, R7.Pin_0, R8.Pin_0, R9.Pin_0
  N14: Composant1.D0/RX, Composant2.connector37
  N15: Composant1.D2, S3.Pin_1, S3.Pin_2
  N16: Composant1.D3_PWM, S1.Pin_1, S1.Pin_2
  N17: Composant1.D4, S2.Pin_1, S2.Pin_2
  N18: Composant1.5V, Composant2.connector39, S1.Pin_3, S1.Pin_4, S2.Pin_3, S2.Pin_4, S3.Pin_3, S3.Pin_4
  N19: 7_Segment_4_Digit_Display1.connector6, R5.Pin_1
  N20: 7_Segment_4_Digit_Display1.connector8, R6.Pin_1
  N21: 7_Segment_4_Digit_Display1.connector9, R2.Pin_1
  N22: 7_Segment_4_Digit_Display1.connector12, R1.Pin_1
