# Fritzing sketch id4185_MIMIZUKU_CIRCUIT_1_0 (saved by Fritzing 0.9.0b)
circuit board: 8.46667cm x 5.64444cm
breadboards: 1

parts:
  Raspberry_Pi1 = Raspberry Pi B rev2
  LCD1 = LCD screen
  RHT1 = Humidity and Temperature Sensor RHT03
  R1 = Resistor [tolerance=±5% resistance=4.7k package=THT]
  R2 = Resistor [tolerance=±5% resistance=4.7k package=THT]
  Part1 = Barometric Pressure Sensor - BMP085 Breakout
  R3 = Trimmer Potentiometer [maximum_resistance=10kΩ package=THT]

nets:
  3V3: Raspberry_Pi1.3V3, Part1.VCC
  5V: Raspberry_Pi1.5V, LCD1.VDD, LCD1.LED+, RHT1.Vcc, R1.Pin_0, R3.leg2
  N1: Raspberry_Pi1.GPIO_2, Part1.SDA
  N2: Raspberry_Pi1.GPIO_3, Raspberry_Pi1.GPIO_4, Part1.SCL
  N3: Raspberry_Pi1.GPIO_23, LCD1.DB4
  N4: Raspberry_Pi1.GPIO_14, RHT1.Data-signal, R2.Pin_1
  N5: Raspberry_Pi1.GPIO_17, LCD1.DB5
  N6: Raspberry_Pi1.GPIO_27, LCD1.DB6
  N7: Raspberry_Pi1.GPIO_22, LCD1.DB7
  N8: Raspberry_Pi1.GPIO_24, LCD1.E
  N9: Raspberry_Pi1.GPIO_25, LCD1.RS
  VSS: LCD1.VSS, LCD1.R/W, LCD1.LED-, RHT1.GND_2, Part1.GND, R3.leg1
  N10: LCD1.V0, R3.wiper
  N11: R1.Pin_1, R2.Pin_0
