# Fritzing sketch id4186_SENSoR_0 (saved by Fritzing 0.9.1b)
breadboards: 1

parts:
  Eleman1 = Arduino Uno (Rev3)
  LED1 = LED - 5mm [color="Red (633nm)" package="5 mm [THT]"]
  LED2 = LED - 5mm [color="Red (633nm)" package="5 mm [THT]"]
  R1 = Resistor [tolerance=±5% resistance=220 package=THT]
  Eleman2 = SRF05 Ultrasonic Rangefinder
  R2 = Resistor [tolerance=±5% resistance=220 package=THT]

nets:
  N1: Eleman1.D10_PWM/SS, LED2.anode
  N2: Eleman1.D11_PWM/MOSI, LED1.anode
  N3: Eleman1.D12/MISO, Eleman2.connector9
  N4: Eleman1.D13/SCK, Eleman2.connector10
  N5: Eleman1.GND, R1.Pin_0, Eleman2.connector11, R2.Pin_0
  N6: Eleman1.VIN, Eleman2.connector8
  N7: LED1.cathode, R2.Pin_1
  N8: LED2.cathode, R1.Pin_1
