# Fritzing sketch id4188_fm_0 (saved by Fritzing 0.7.10b)
breadboards: 1

parts:
  MIC1 = Microphone
  9V = Battery block 9V
  1MR2 = Resistor [tolerance=±5% resistance=1M package=THT]
  10kR3 = Resistor [tolerance=±5% resistance=10k package=THT]
  68kR1 = Resistor [tolerance=±5% resistance=68k package=THT]
  47kR4 = Resistor [tolerance=±5% resistance=47k package=THT]
  100R5 = Resistor [tolerance=±5% resistance=100 package=THT]
  22nC1 = Ceramic Capacitor [capacitance=22nF package="100 mil [THT, multilayer]"]
  100nC2 = Ceramic Capacitor [capacitance=100nF voltage=6.3V package="100 mil [THT, multilayer]"]
  1nfC3 = Ceramic Capacitor [capacitance=1nF package="100 mil [THT, multilayer]"]
  33nC4 = Ceramic Capacitor [capacitance=33pF package="100 mil [THT, multilayer]"]
  15pC5 = Ceramic Capacitor [capacitance=15pF package="100 mil [THT, multilayer]"]
  68kR6 = Resistor [tolerance=±5% resistance=68k package=THT]
  10pC6 = Ceramic Capacitor [capacitance=10pF package="100 mil [THT, multilayer]"]
  15pC7 = Ceramic Capacitor [capacitance=15pF package="100 mil [THT, multilayer]"]
  22nC8 = Ceramic Capacitor [capacitance=22nF package="100 mil [THT, multilayer]"]
  ANT1 = Antenna
  L1 = Inductor [package="400 mil [THT]"]
  T1 = NPN-Transistor [package="SOT-23 [SMD]"]
  T2 = NPN-Transistor [package="SOT-23 [SMD]"]
  T3 = NPN-Transistor [package="SOT-23 [SMD]"]
  4turns = Inductor [package="400 mil [THT]"]

nets:
  N1: MIC1.pin1, MIC1.pin2, 9V.-, 9V.+, 1MR2.Pin_0, 1MR2.Pin_1, 10kR3.Pin_0, 10kR3.Pin_1, 68kR1.Pin_0, 68kR1.Pin_1, 47kR4.Pin_0, 47kR4.Pin_1, 100R5.Pin_0, 100R5.Pin_1, 22nC1.0, 22nC1.1, 100nC2.0, 100nC2.1, 1nfC3.0, 1nfC3.1, 33nC4.0, 33nC4.1, 15pC5.0, 15pC5.1, 68kR6.Pin_0, 68kR6.Pin_1, 10pC6.0, 10pC6.1, 15pC7.0, 15pC7.1, 22nC8.0, 22nC8.1, ANT1.antenna_lead, L1.pin_0, L1.pin_1, T1.2, T1.0, T1.1, T2.2, T2.0, T2.1, T3.2, T3.0, T3.1, 4turns.pin_0, 4turns.pin_1

notes:
  -
  +
  FmTrans
