# Fritzing sketch id4193_TIPE_(1)_0 (saved by Fritzing 0.9.3b)
breadboards: 1

parts:
  Composant1 = Arduino Uno (Rev3)
  M4 = Stepper Motor - Bipolar
  Composant1_2 = Arduino Uno (Rev3)
  LCD1 = LCD screen  # not connected

nets:
  N1: Composant1.D8, M4.B
  N2: Composant1.D9_PWM, M4.C
  N3: Composant1.D10_PWM/SS, M4.A
  N4: Composant1.D0/RX, Composant1_2.D1/TX
  N5: Composant1.D1/TX, Composant1_2.D0/RX
  N6: Composant1.D7, M4.D
  GND: Composant1.GND, Composant1_2.GND
