# Fritzing sketch id4194_Tipo_clave_morse_0 (saved by Fritzing 0.9.2b)
breadboards: 1

parts:
  Parte1 = Arduino Uno (Rev3)
  LED1 = LED - 5mm [color="Red (633nm)" package="5 mm [THT]"]
  LED2 = LED - 5mm [color="Red (633nm)" package="5 mm [THT]"]
  LED3 = LED - 5mm [color="Red (633nm)" package="5 mm [THT]"]
  R1 = Resistor [tolerance=±5% resistance=220 package=THT]
  R2 = Resistor [tolerance=±5% resistance=220 package=THT]
  R3 = Resistor [tolerance=±5% resistance=220 package=THT]
  S1 = Pushbutton [package="[THT]"]
  R4 = Resistor [tolerance=±5% resistance=220 package=THT]

nets:
  N1: Parte1.D8, S1.Pin_1, S1.Pin_2, R4.Pin_0
  N2: Parte1.GND, LED1.cathode, LED2.cathode, LED3.cathode, R4.Pin_1
  N3: Parte1.D5_PWM, R1.Pin_0
  N4: Parte1.D6_PWM, R2.Pin_0
  N5: Parte1.D7, R3.Pin_0
  N6: Parte1.5V, S1.Pin_3, S1.Pin_4
  N7: LED1.anode, R3.Pin_1
  N8: LED2.anode, R2.Pin_1
  N9: LED3.anode, R1.Pin_1
