# Fritzing sketch id4195_pprojekt_0 (saved by Fritzing 0.9.3b)
breadboards: 2

parts:
  Part1 = Arduino Mega 2560 (Rev3)
  R1 = Resistor [tolerance=±5% resistance=220 package=THT]
  LCD1 = LCD screen
  R2 = Rotary Potentiometer (Small) [maximum_resistance=100kΩ package=THT]
  T1 = LM35 Temperature Sensor [package="TO92 [THT]"]
  R3 = Resistor [tolerance=±5% resistance=220 package=THT]
  R4 = Resistor [tolerance=±5% resistance=220 package=THT]
  R5 = Resistor [tolerance=±5% resistance=220 package=THT]
  R6 = Resistor [tolerance=±5% resistance=220 package=THT]
  R7 = Resistor [tolerance=±5% resistance=220 package=THT]
  R8 = Resistor [tolerance=±5% resistance=220 package=THT]
  R9 = Resistor [tolerance=±5% resistance=220 package=THT]
  R10 = Resistor [tolerance=±5% resistance=220 package=THT]
  R11 = Resistor [tolerance=±5% resistance=220 package=THT]
  R12 = Resistor [tolerance=±5% resistance=220 package=THT]
  S1 = Pushbutton [package="[THT]"]
  LED1 = LED - 5mm [color="Red (633nm)" package="5 mm [THT]"]
  LED2 = LED - 5mm [color="Red (633nm)" package="5 mm [THT]"]
  LED3 = LED - 5mm [color="Red (633nm)" package="5 mm [THT]"]
  LED4 = LED - 5mm [color="Red (633nm)" package="5 mm [THT]"]
  LED5 = LED - 5mm [color="Red (633nm)" package="5 mm [THT]"]
  LED6 = LED - 5mm [color="Red (633nm)" package="5 mm [THT]"]
  LED7 = LED - 5mm [color="Red (633nm)" package="5 mm [THT]"]
  LED8 = LED - 5mm [color="Red (633nm)" package="5 mm [THT]"]
  LED9 = LED - 5mm [color="Red (633nm)" package="5 mm [THT]"]
  LED10 = LED - 5mm [color="Red (633nm)" package="5 mm [THT]"]
  LED11 = LED - 5mm [color="Red (633nm)" package="5 mm [THT]"]

nets:
  N1: Part1.A0, T1.Vout
  GND: Part1.GND, LCD1.VSS, LCD1.R/W, LCD1.LED-, R2.leg2, T1.GND, S1.Pin_3, S1.Pin_4, LED1.cathode, LED2.cathode, LED3.cathode, LED4.cathode, LED5.cathode, LED6.cathode, LED7.cathode, LED8.cathode, LED9.cathode, LED10.cathode, LED11.cathode
  5V: Part1.5V, LCD1.VDD, R2.leg1, T1.+Vs
  N2: Part1.D0_RX0, LCD1.RS
  N3: Part1.D1_TX0, LCD1.E
  N4: Part1.D2_PWM, LCD1.DB4
  N5: Part1.D3_PWM, LCD1.DB5
  N6: Part1.D4_PWM, LCD1.DB6
  N7: Part1.D5_PWM, LCD1.DB7
  N8: Part1.D33, R12.Pin_1
  N9: Part1.D35, R1.Pin_1, R4.Pin_0, LED3.anode
  N10: Part1.D37, R3.Pin_1
  N11: Part1.D39, R4.Pin_1
  N12: Part1.D41, R7.Pin_1
  N13: Part1.D43, R6.Pin_1
  N14: Part1.D45, R5.Pin_1
  N15: Part1.D47, R8.Pin_1
  N16: Part1.D49, R9.Pin_1
  N17: Part1.D51, R10.Pin_1
  N18: Part1.D52, S1.Pin_1, S1.Pin_2
  N19: Part1.D53, R11.Pin_1
  N20: R1.Pin_0, LED2.anode
  N21: LCD1.V0, R2.wiper
  N22: R3.Pin_0, LED4.anode
  N23: R5.Pin_0, LED7.anode
  N24: R6.Pin_0, LED6.anode
  N25: R7.Pin_0, LED5.anode
  N26: R8.Pin_0, LED8.anode
  N27: R9.Pin_0, LED9.anode
  N28: R10.Pin_0, LED10.anode
  N29: R11.Pin_0, LED11.anode
  N30: R12.Pin_0, LED1.anode
