# Fritzing sketch id4197_TLC5940_and_Arduino_0 (saved by Fritzing 0.7.4b)
breadboards: 1

parts:
  Arduino1 = Arduino
  IC1 = IC, DIP package, 28 pins [chip_label=TLC5940 spacing=300mil]
  R1 = Resistor [tolerance=±5% resistance=10k package=THT]
  R2 = Resistor [tolerance=±5% resistance=2.2k package=THT]
  LED1 = LED - 3mm [color="Red (633nm)" package="3 mm [THT]"]
  LED2 = LED - 3mm [color="Red (633nm)" package="3 mm [THT]"]
  LED3 = LED - 3mm [color="Red (633nm)" package="3 mm [THT]"]

nets:
  N1: Arduino1.D13, IC1.pin25
  N2: Arduino1.D11, IC1.pin26
  N3: Arduino1.D10, IC1.pin23, R1.Pin_0
  N4: Arduino1.D9, IC1.pin24
  N5: Arduino1.D3, IC1.pin18
  N6: Arduino1.+5V, IC1.pin19, IC1.pin21, R1.Pin_1, LED1.anode, LED2.anode, LED3.anode
  N7: Arduino1.GND, IC1.pin22, IC1.pin27, R2.Pin_1
  N8: IC1.pin1, LED2.cathode
  N9: IC1.pin2, LED3.cathode
  N10: IC1.pin20, R2.Pin_0
  N11: IC1.pin28, LED1.cathode

notes:
  put LEDs in remaining channels
