# Fritzing sketch id4198_TLC_Breakout_0 (saved by Fritzing 0.7.10b)
breadboards: 1

parts:
  J1 = female pin header, 3 pins [form="♀ (female)"]
  J2 = female pin header, 3 pins [form="♀ (female)"]
  J3 = female pin header, 3 pins [form="♀ (female)"]
  J4 = female pin header, 3 pins [form="♀ (female)"]
  J5 = female pin header, 3 pins [form="♀ (female)"]
  J6 = female pin header, 3 pins [form="♀ (female)"]
  J7 = female pin header, 3 pins [form="♀ (female)"]
  J8 = female pin header, 3 pins [form="♀ (female)"]
  J9 = female pin header, 3 pins [form="♀ (female)"]
  J10 = female pin header, 3 pins [form="♀ (female)"]
  J11 = female pin header, 3 pins [form="♀ (female)"]
  J12 = female pin header, 3 pins [form="♀ (female)"]
  J13 = female pin header, 3 pins [form="♀ (female)"]
  J14 = female pin header, 3 pins [form="♀ (female)"]
  J15 = female pin header, 3 pins [form="♀ (female)"]
  J16 = female pin header, 3 pins [form="♀ (female)"]
  R1 = Resistor [tolerance=±5% resistance=220 package=THT]
  R2 = Resistor [tolerance=±5% resistance=220 package=THT]
  R3 = Resistor [tolerance=±5% resistance=220 package=THT]
  R4 = Resistor [tolerance=±5% resistance=220 package=THT]
  R5 = Resistor [tolerance=±5% resistance=220 package=THT]
  R6 = Resistor [tolerance=±5% resistance=220 package=THT]
  R7 = Resistor [tolerance=±5% resistance=220 package=THT]
  R8 = Resistor [tolerance=±5% resistance=220 package=THT]
  R9 = Resistor [tolerance=±5% resistance=220 package=THT]
  R10 = Resistor [tolerance=±5% resistance=220 package=THT]
  R11 = Resistor [tolerance=±5% resistance=220 package=THT]
  R12 = Resistor [tolerance=±5% resistance=220 package=THT]
  R13 = Resistor [tolerance=±5% resistance=220 package=THT]
  R14 = Resistor [tolerance=±5% resistance=220 package=THT]
  R15 = Resistor [tolerance=±5% resistance=220 package=THT]
  R16 = Resistor [tolerance=±5% resistance=220 package=THT]
  IC1 = IC, DIP package, 28 pins [chip_label=IC]
  U1 = Voltage Regulator - 5V [package="TO220 [THT]"]
  J17 = male pin header, 7 pins [form="♂ (male)"]
  J18 = male pin header, 7 pins [form="♂ (male)"]
  R17 = Resistor [tolerance=±5% resistance=220 package=THT]
  R18 = Resistor [tolerance=±5% resistance=220 package=THT]
  C1 = Ceramic Capacitor [capacitance=100nF package="100 mil [THT, multilayer]"]
  C2 = Electrolytic Capacitor [capacitance=1µF package="100 mil [THT, electrolytic]"]
  C3 = Electrolytic Capacitor [capacitance=1µF package="100 mil [THT, electrolytic]"]
  J19 = female pin header, 2 pins [form="♀ (female)"]
  J20 = female pin header, 2 pins [form="♀ (female)"]
  LED1 = LED - 3mm [color="Red (633nm)" package="3 mm [THT]"]
  R19 = Resistor [tolerance=±5% resistance=220 package=THT]

nets:
  N1: J1.pin1, R1.Pin_0, IC1.pin28
  N2: J1.pin2, J2.pin2, J3.pin2, J4.pin2, J5.pin2, J6.pin2, J7.pin2, J8.pin2, J9.pin2, J10.pin2, J11.pin2, J12.pin2, J13.pin2, J14.pin2, J15.pin2, J16.pin2, R1.Pin_1, R2.Pin_1, R3.Pin_1, R4.Pin_1, R5.Pin_1, R6.Pin_1, R7.Pin_1, R8.Pin_1, R9.Pin_1, R10.Pin_1, R11.Pin_1, R12.Pin_1, R13.Pin_1, R14.Pin_1, R15.Pin_1, R16.Pin_1, IC1.pin19, IC1.pin21, U1.output_voltage, J17.pin3, J18.pin3, C1.1, C3.+, R19.Pin_1
  N3: J1.pin3, J2.pin3, J3.pin3, J4.pin3, J5.pin3, J6.pin3, J7.pin3, J8.pin3, J9.pin3, J10.pin3, J11.pin3, J12.pin3, J13.pin3, J14.pin3, J15.pin3, J16.pin3, IC1.pin22, IC1.pin27, U1.GND, J17.pin4, J18.pin4, R17.Pin_1, R18.Pin_1, C1.0, C2.-, C3.-, J19.pin1, J20.pin2, LED1.cathode
  N4: J2.pin1, R2.Pin_0, IC1.pin1
  N5: J3.pin1, R4.Pin_0, IC1.pin3
  N6: J4.pin1, R3.Pin_0, IC1.pin2
  N7: J5.pin1, R6.Pin_0, IC1.pin7
  N8: J6.pin1, R7.Pin_0, IC1.pin6
  N9: J7.pin1, R8.Pin_0, IC1.pin5
  N10: J8.pin1, R5.Pin_0, IC1.pin4
  N11: J9.pin1, R12.Pin_0, IC1.pin11
  N12: J10.pin1, R10.Pin_0, IC1.pin14
  N13: J11.pin1, R16.Pin_0, IC1.pin9
  N14: J12.pin1, R11.Pin_0, IC1.pin13
  N15: J13.pin1, R9.Pin_0, IC1.pin8
  N16: J14.pin1, R13.Pin_0, IC1.pin15
  N17: J15.pin1, R15.Pin_0, IC1.pin12
  N18: J16.pin1, R14.Pin_0, IC1.pin10
  N19: IC1.pin16, J20.pin1
  N20: IC1.pin17, J17.pin1
  N21: IC1.pin18, J17.pin2, J18.pin2
  N22: IC1.pin20, R17.Pin_0, R18.Pin_0
  N23: IC1.pin23, J17.pin5, J18.pin5
  N24: IC1.pin24, J17.pin6, J18.pin6
  N25: IC1.pin25, J17.pin7, J18.pin7
  N26: IC1.pin26, J18.pin1
  N27: U1.input_voltage, C2.+, J19.pin2
  N28: LED1.anode, R19.Pin_0
