# Fritzing sketch id4199_TLC5940_Breakout_WithAtmega328_0 (saved by Fritzing 0.8.3b)
circuit board: 10cm x 10cm

parts:
  R1 = Resistor [tolerance=±5% resistance=10k package=THT]
  R2 = Resistor [tolerance=±5% resistance=10k package=THT]
  J10 = Screw terminal - 2 pins [package=THT]
  J11 = Screw terminal - 2 pins [package=THT]
  J12 = Screw terminal - 2 pins [package=THT]
  J13 = Screw terminal - 2 pins [package=THT]
  J14 = Screw terminal - 2 pins [package=THT]
  J15 = Screw terminal - 2 pins [package=THT]
  J16 = Screw terminal - 2 pins [package=THT]
  J17 = Screw terminal - 2 pins [package=THT]
  R3 = Resistor [tolerance=±5% resistance=10k package=THT]
  R4 = Resistor [tolerance=±5% resistance=10k package=THT]
  R5 = Resistor [tolerance=±5% resistance=10k package=THT]
  R6 = Resistor [tolerance=±5% resistance=10k package=THT]
  R7 = Resistor [tolerance=±5% resistance=10k package=THT]
  R8 = Resistor [tolerance=±5% resistance=10k package=THT]
  R10 = Resistor [tolerance=±5% resistance=10k package=THT]
  R11 = Resistor [tolerance=±5% resistance=10k package=THT]
  R12 = Resistor [tolerance=±5% resistance=10k package=THT]
  R13 = Resistor [tolerance=±5% resistance=10k package=THT]
  R14 = Resistor [tolerance=±5% resistance=10k package=THT]
  R15 = Resistor [tolerance=±5% resistance=10k package=THT]
  R16 = Resistor [tolerance=±5% resistance=10k package=THT]
  TLC5940 = Packages: [package=dil28-3]
  J19 = female pin header, 8 pins [form="♀ (female)"]
  J18 = female pin header, 8 pins [form="♀ (female)"]
  R17 = Resistor [tolerance=±5% resistance=10k package=THT]
  R18 = Resistor [tolerance=±5% resistance=10k package=THT]
  R9 = Resistor [tolerance=±5% resistance=10k package=THT]
  Arduino_StandAlone_By_FLPRO2 = atmega328 [package=dip]
  C5 = Ceramic Disk Capacitor [package=THT]
  C6 = Ceramic Disk Capacitor [package=THT]
  U10 = Mystery Part - 6 pins [package=THT]
  U12 = Mystery Part - 4 pins [package=THT]
  U13 = Mystery Part - 5 pins [package=THT]
  U14 = Voltage Regulator - 5V [package="TO220 [THT]"]
  C8 = Capacitor [package=cap-pth-small2]
  C7 = Electrolytic Capacitor [capacitance=10μF package="100 mil [THT, electrolytic]"]
  S6 = Toggle Switch [package=THT]
  XTAL3 = Crystal [frequency="16 Mhz" package=THT]
  J20 = Power Jack [package=power_jack_pth_lock]
  C9 = Electrolytic Capacitor [capacitance=10μF package="100 mil [THT, electrolytic]"]
  J21 = female pin header, 2 pins [form="♀ (female)"]
  J22 = female pin header, 2 pins [form="♀ (female)"]
  Y1 = Resonator [package=resonator-pth]
  R55 = Resistor [tolerance=±5% resistance=220 package=THT]
  LED1 = LED - 3mm [color="Red (633nm)" package="3 mm [THT]"]
  J41 = Screw terminal - 2 pins [package=THT]
  J40 = double row male pin header, 6 pins [form="♂ (male)"]
  R74 = Resistor [tolerance=±5% resistance=220 package=THT]  # not connected
  C12 = Capacitor [package=cap-pth-small2]
  U11 = Mystery Part - 6 pins [package=THT]
  R76 = Resistor [tolerance=±5% resistance=220 package=THT]
  LED2 = LED - 3mm [color="Red (633nm)" package="3 mm [THT]"]
  J52 = female pin header, 3 pins [form="♀ (female)"]
  J53 = female pin header, 3 pins [form="♀ (female)"]
  R94 = Resistor [tolerance=±5% resistance=220 package=THT]  # not connected
  C13 = Capacitor [package=cap-pth-small2]
  TLC5940_2 = Packages: [package=dil28-3]
  R95 = Resistor [tolerance=±5% resistance=10k package=THT]
  R96 = Resistor [tolerance=±5% resistance=10k package=THT]
  R97 = Resistor [tolerance=±5% resistance=10k package=THT]
  R98 = Resistor [tolerance=±5% resistance=10k package=THT]
  R99 = Resistor [tolerance=±5% resistance=10k package=THT]
  R100 = Resistor [tolerance=±5% resistance=10k package=THT]
  R101 = Resistor [tolerance=±5% resistance=10k package=THT]
  R102 = Resistor [tolerance=±5% resistance=10k package=THT]
  R103 = Resistor [tolerance=±5% resistance=10k package=THT]
  R104 = Resistor [tolerance=±5% resistance=10k package=THT]
  R105 = Resistor [tolerance=±5% resistance=10k package=THT]
  R106 = Resistor [tolerance=±5% resistance=10k package=THT]
  R107 = Resistor [tolerance=±5% resistance=10k package=THT]
  R108 = Resistor [tolerance=±5% resistance=10k package=THT]
  R109 = Resistor [tolerance=±5% resistance=10k package=THT]
  R110 = Resistor [tolerance=±5% resistance=10k package=THT]
  R111 = Resistor [tolerance=±5% resistance=10k package=THT]
  R112 = Resistor [tolerance=±5% resistance=10k package=THT]
  J66 = Screw terminal - 2 pins [package=THT]
  J67 = Screw terminal - 2 pins [package=THT]
  J68 = Screw terminal - 2 pins [package=THT]
  J69 = Screw terminal - 2 pins [package=THT]
  J70 = Screw terminal - 2 pins [package=THT]
  J71 = Screw terminal - 2 pins [package=THT]
  J72 = Screw terminal - 2 pins [package=THT]
  J73 = Screw terminal - 2 pins [package=THT]
  J74 = female pin header, 8 pins [form="♀ (female)"]
  J75 = female pin header, 3 pins [form="♀ (female)"]
  J76 = female pin header, 3 pins [form="♀ (female)"]
  J77 = female pin header, 8 pins [form="♀ (female)"]
  S3 = Pushbutton [package="[THT]"]
  R113 = Resistor [tolerance=±5% resistance=220 package=THT]

nets:
  N1: R1.Pin_0, J10.pin1, TLC5940.OUT15
  N2: R1.Pin_1, R2.Pin_1, R3.Pin_1, R4.Pin_1, R5.Pin_1, R6.Pin_1, R7.Pin_1, R8.Pin_1, R10.Pin_1, R11.Pin_1, R12.Pin_1, R13.Pin_1, R14.Pin_1, R15.Pin_1, R16.Pin_1, TLC5940.DCPRG, TLC5940.VCC, J19.pin5, J18.pin5, R18.Pin_0, R9.Pin_1, C8.1
  N3: R2.Pin_0, J10.pin2, TLC5940.OUT14
  N4: J11.pin1, R4.Pin_0, TLC5940.OUT13
  N5: J11.pin2, R3.Pin_0, TLC5940.OUT12
  N6: J12.pin1, R6.Pin_0, TLC5940.OUT11
  N7: J12.pin2, R7.Pin_0, TLC5940.OUT10
  N8: J13.pin1, R11.Pin_0, TLC5940.OUT7
  N9: J13.pin2, TLC5940.OUT6, R9.Pin_0
  N10: J14.pin1, R8.Pin_0, TLC5940.OUT9
  N11: J14.pin2, R5.Pin_0, TLC5940.OUT8
  N12: J15.pin1, R10.Pin_0, TLC5940.OUT5
  N13: J15.pin2, R12.Pin_0, TLC5940.OUT4
  N14: J16.pin1, R14.Pin_0, TLC5940.OUT1
  N15: J16.pin2, R16.Pin_0, TLC5940.OUT0
  N16: J17.pin1, R15.Pin_0, TLC5940.OUT3
  N17: J17.pin2, R13.Pin_0, TLC5940.OUT2
  N18: TLC5940.SOUT, TLC5940.SIN, J19.pin3, J18.pin3
  N19: TLC5940.GSCLK, J19.pin4, J18.pin4
  N20: TLC5940.IREF, R17.Pin_0
  N21: TLC5940.GND, TLC5940.VPRG, J19.pin6, J18.pin6, R17.Pin_1, C8.2
  N22: TLC5940.BLANK, J19.pin7, J18.pin7, R18.Pin_1
  N23: TLC5940.XLAT, J19.pin2, J18.pin2
  N24: TLC5940.SCLK, J19.pin1, J18.pin1
  N25: Arduino_StandAlone_By_FLPRO2.RESET, J40.pin3, S3.Pin_1, S3.Pin_2, R113.Pin_1
  N26: Arduino_StandAlone_By_FLPRO2.D0_(RX), U13.leg5
  N27: Arduino_StandAlone_By_FLPRO2.D1_(TX), U13.leg4
  N28: Arduino_StandAlone_By_FLPRO2.D2, U13.leg3
  N29: Arduino_StandAlone_By_FLPRO2.D3_(PWM), U13.leg2
  N30: Arduino_StandAlone_By_FLPRO2.D4, U13.leg1
  N31: Arduino_StandAlone_By_FLPRO2.VCC, Arduino_StandAlone_By_FLPRO2.AVCC, U14.output_voltage, C7.+, J21.pin2, J22.pin2, J40.pin6, LED2.anode, R113.Pin_0
  GND: Arduino_StandAlone_By_FLPRO2.GND, C5.pin_0, C6.pin_1, U14.GND, C7.-, J20.GND, J20.GNDBREAK, C9.-, J21.pin1, J22.pin1, Y1.2, LED1.cathode, J41.pin2, J40.pin4, C12.1, R76.Pin_0, S3.Pin_3, S3.Pin_4
  N32: Arduino_StandAlone_By_FLPRO2.XLAT1, C6.pin_0, XTAL3.pin_1, Y1.1
  N33: Arduino_StandAlone_By_FLPRO2.XLAT2, C5.pin_1, XTAL3.pin_0, Y1.3
  N34: Arduino_StandAlone_By_FLPRO2.D5_(PWM), U12.leg4
  N35: Arduino_StandAlone_By_FLPRO2.D6_(PWM), U12.leg3
  N36: Arduino_StandAlone_By_FLPRO2.D7, U12.leg2
  N37: Arduino_StandAlone_By_FLPRO2.D8, U12.leg1
  N38: Arduino_StandAlone_By_FLPRO2.D9_(PWM), U11.leg6
  N39: Arduino_StandAlone_By_FLPRO2.D10_(PWM), U11.leg5
  N40: Arduino_StandAlone_By_FLPRO2.D11_(PWM), J40.pin5, U11.leg4
  N41: Arduino_StandAlone_By_FLPRO2.D12, J40.pin1, U11.leg3
  N42: Arduino_StandAlone_By_FLPRO2.D13, R55.Pin_0, J40.pin2, U11.leg2
  N43: Arduino_StandAlone_By_FLPRO2.AREF, C12.2, U11.leg1
  N44: Arduino_StandAlone_By_FLPRO2.A0, U10.leg6
  N45: Arduino_StandAlone_By_FLPRO2.A1, U10.leg5
  N46: Arduino_StandAlone_By_FLPRO2.A2, U10.leg4
  N47: Arduino_StandAlone_By_FLPRO2.A3, U10.leg3
  N48: Arduino_StandAlone_By_FLPRO2.A4, U10.leg2
  N49: Arduino_StandAlone_By_FLPRO2.A5, U10.leg1
  N50: U14.input_voltage, S6.L2, C9.+
  N51: S6.COM, J20.PWR, J41.pin1
  N52: R55.Pin_1, LED1.anode
  N53: R76.Pin_1, LED2.cathode
  N54: J52.pin1, J53.pin1
  N55: J52.pin2, J53.pin2
  N56: J52.pin3, J53.pin3
  N57: C13.1, TLC5940_2.DCPRG, TLC5940_2.VCC, R95.Pin_0, R97.Pin_1, R98.Pin_1, R99.Pin_1, R100.Pin_1, R101.Pin_1, R102.Pin_1, R103.Pin_1, R104.Pin_1, R105.Pin_1, R106.Pin_1, R107.Pin_1, R108.Pin_1, R109.Pin_1, R110.Pin_1, R111.Pin_1, R112.Pin_1, J74.pin5, J77.pin5
  N58: C13.2, TLC5940_2.GND, TLC5940_2.VPRG, R96.Pin_1, J74.pin6, J77.pin6
  N59: TLC5940_2.OUT1, R99.Pin_0, J67.pin1
  N60: TLC5940_2.OUT2, R100.Pin_0, J66.pin2
  N61: TLC5940_2.OUT3, R98.Pin_0, J66.pin1
  N62: TLC5940_2.OUT4, R101.Pin_0, J68.pin2
  N63: TLC5940_2.OUT5, R103.Pin_0, J68.pin1
  N64: TLC5940_2.OUT6, R104.Pin_0, J70.pin2
  N65: TLC5940_2.OUT7, R102.Pin_0, J70.pin1
  N66: TLC5940_2.OUT8, R108.Pin_0, J69.pin2
  N67: TLC5940_2.OUT9, R105.Pin_0, J69.pin1
  N68: TLC5940_2.OUT10, R106.Pin_0, J71.pin2
  N69: TLC5940_2.OUT11, R107.Pin_0, J71.pin1
  N70: TLC5940_2.OUT12, R110.Pin_0, J72.pin2
  N71: TLC5940_2.OUT13, R109.Pin_0, J72.pin1
  N72: TLC5940_2.OUT14, R111.Pin_0, J73.pin2
  N73: TLC5940_2.OUT15, R112.Pin_0, J73.pin1
  N74: TLC5940_2.SOUT, TLC5940_2.SIN, J74.pin3, J77.pin3
  N75: TLC5940_2.GSCLK, J74.pin4, J77.pin4
  N76: TLC5940_2.IREF, R96.Pin_0
  N77: TLC5940_2.BLANK, R95.Pin_1, J74.pin7, J77.pin7
  N78: TLC5940_2.XLAT, J74.pin2, J77.pin2
  N79: TLC5940_2.SCLK, J74.pin1, J77.pin1
  N80: TLC5940_2.OUT0, R97.Pin_0, J67.pin2
  N81: J75.pin1, J76.pin1
  N82: J75.pin2, J76.pin2
  N83: J75.pin3, J76.pin3

notes:
  GND
  VCC
  GSLCK
  SIN
  SOUT
  XLAT
  SLCK
  BLANK
  TLC5940NT
  marinus@noweverywhere.ca
  MISO
  CLK
  RST
  V+
  PWR
  AREF
  OUT_0
  OUT_15
  0
  1
  2
  3
  4
  5
  6
  7
  8
  9
  10
  11
  12
  13
  14
  15
  RX
  TX
  D2
  ~D3
  D4
  ~D5
  ~D6
  D7
  D8
  D9~
  D10~
  D11~
  D12
  D13
  A0
  A1
  A2
  A3
  A4
