# Fritzing sketch id419_Binuhr_Fritzing_2_0 (saved by Fritzing 0.8.7b)
circuit board: 7.89746cm x 5.74555cm
breadboards: 2

parts:
  sec1 = LED - 5mm [color="Red (633nm)" package="5 mm [THT]"]
  sec2 = LED - 5mm [color="Red (633nm)" package="5 mm [THT]"]
  sec4 = LED - 5mm [color="Red (633nm)" package="5 mm [THT]"]
  sec8 = LED - 5mm [color="Red (633nm)" package="5 mm [THT]"]
  sec16 = LED - 5mm [color="Red (633nm)" package="5 mm [THT]"]
  sec32 = LED - 5mm [color="Red (633nm)" package="5 mm [THT]"]
  min1 = LED - 5mm [color="Yellow (595nm)" package="5 mm [THT]"]
  min2 = LED - 5mm [color="Yellow (595nm)" package="5 mm [THT]"]
  min4 = LED - 5mm [color="Yellow (595nm)" package="5 mm [THT]"]
  min8 = LED - 5mm [color="Yellow (595nm)" package="5 mm [THT]"]
  min16 = LED - 5mm [color="Yellow (595nm)" package="5 mm [THT]"]
  min32 = LED - 5mm [color="Yellow (595nm)" package="5 mm [THT]"]
  U2 = PCF8574 [package="DIP16 [THT]"]
  U3 = PCF8574 [package="DIP16 [THT]"]
  U1 = PCF8574 [package="DIP16 [THT]"]
  hor8 = LED - 5mm [color="Green (570nm)" package="5 mm [THT]"]
  hor4 = LED - 5mm [color="Green (570nm)" package="5 mm [THT]"]
  hor2 = LED - 5mm [color="Green (570nm)" package="5 mm [THT]"]
  hor1 = LED - 5mm [color="Green (570nm)" package="5 mm [THT]"]
  Bauteil1 = Arduino Uno (Rev3)
  SetH = Pushbutton [package="[THT]"]
  Res = Pushbutton [package="[THT]"]
  SetM = Pushbutton [package="[THT]"]
  R2 = Resistor [tolerance=±1% resistance=4.7k package=THT]
  R1 = Resistor [tolerance=±1% resistance=4.7k package=THT]

nets:
  N1: sec1.cathode, U3.P0
  VCC: sec1.anode, sec2.anode, sec4.anode, sec8.anode, sec16.anode, sec32.anode, min1.anode, min2.anode, min4.anode, min8.anode, min16.anode, min32.anode, U2.A0, U2.VCC, U3.VCC, U1.A0, U1.A1, U1.VCC, hor8.anode, hor4.anode, hor2.anode, hor1.anode, Bauteil1.5V, R2.Pin_1, R1.Pin_1
  N2: sec2.cathode, U3.P1
  N3: sec4.cathode, U3.P2
  N4: sec8.cathode, U3.P3
  N5: sec16.cathode, U3.P4
  N6: sec32.cathode, U3.P5
  N7: min1.cathode, U2.P0
  N8: min2.cathode, U2.P1
  N9: min4.cathode, U2.P2
  N10: min8.cathode, U2.P3
  N11: min16.cathode, U2.P4
  N12: min32.cathode, U2.P5
  GND: U2.A1, U2.A3, U2.GND, U3.A0, U3.A1, U3.A3, U3.GND, U1.A3, U1.GND, Bauteil1.GND, SetH.Pin_1, SetH.Pin_2, SetM.Pin_1, SetM.Pin_2
  N13: U2.SCL, U3.SCL, U1.SCL, Bauteil1.A5/SCL, R2.Pin_0
  N14: U2.SDA, U3.SDA, U1.SDA, Bauteil1.A4/SDA, R1.Pin_0
  N15: U1.P0, hor1.cathode
  N16: U1.P1, hor2.cathode
  N17: U1.P2, hor4.cathode
  N18: U1.P3, hor8.cathode
  N19: Bauteil1.D2, SetM.Pin_3, SetM.Pin_4
  N20: Bauteil1.D3_PWM, SetH.Pin_3, SetH.Pin_4
  N21: Bauteil1.D4, Res.Pin_3, Res.Pin_4
  N22: Bauteil1.RESET, Res.Pin_1, Res.Pin_2
