# Fritzing sketch id41_16_LED_Hookup_0 (saved by Fritzing 0.7.10b)
breadboards: 1

parts:
  Arduino1 = Arduino
  R1 = Resistor [tolerance=±5% resistance=10k package=THT]
  R2 = Resistor [tolerance=±5% resistance=10k package=THT]
  R3 = Resistor [tolerance=±5% resistance=10k package=THT]
  R4 = Resistor [tolerance=±5% resistance=10k package=THT]
  R5 = Resistor [tolerance=±5% resistance=10k package=THT]
  R6 = Resistor [tolerance=±5% resistance=10k package=THT]
  R7 = Resistor [tolerance=±5% resistance=10k package=THT]
  R8 = Resistor [tolerance=±5% resistance=10k package=THT]
  R9 = Resistor [tolerance=±5% resistance=10k package=THT]
  R10 = Resistor [tolerance=±5% resistance=10k package=THT]
  R11 = Resistor [tolerance=±5% resistance=10k package=THT]
  R12 = Resistor [tolerance=±5% resistance=10k package=THT]
  R13 = Resistor [tolerance=±5% resistance=10k package=THT]
  R14 = Resistor [tolerance=±5% resistance=10k package=THT]
  R15 = Resistor [tolerance=±5% resistance=10k package=THT]
  R16 = Resistor [tolerance=±5% resistance=10k package=THT]
  LED2 = red smd LED [package="1206 [SMD]"]
  LED8 = red smd LED [package="1206 [SMD]"]
  LED10 = red smd LED [package="1206 [SMD]"]
  LED16 = red smd LED [package="1206 [SMD]"]
  LED9 = white smd LED [package="1206 [SMD]"]
  LED1 = white smd LED [package="1206 [SMD]"]
  LED3 = Blue smd LED [package="1206 [SMD]"]
  LED11 = Blue smd LED [package="1206 [SMD]"]
  LED5 = green smd LED [package="1206 [SMD]"]
  LED12 = green smd LED [package="1206 [SMD]"]
  LED4 = white smd LED [package="1206 [SMD]"]
  LED13 = white smd LED [package="1206 [SMD]"]
  LED7 = Blue smd LED [package="1206 [SMD]"]
  LED15 = Blue smd LED [package="1206 [SMD]"]
  LED17 = green smd LED [package="1206 [SMD]"]
  LED18 = green smd LED [package="1206 [SMD]"]

nets:
  N1: Arduino1.GND, LED2.cathode, LED8.cathode, LED10.cathode, LED16.cathode, LED9.cathode, LED1.cathode, LED3.cathode, LED11.cathode, LED5.cathode, LED12.cathode, LED4.cathode, LED13.cathode, LED7.cathode, LED15.cathode, LED17.cathode, LED18.cathode
  N2: Arduino1.D13, R1.Pin_1, R9.Pin_1
  N3: Arduino1.D12, R2.Pin_1, R10.Pin_1
  N4: Arduino1.D11, R3.Pin_1, R11.Pin_1
  N5: Arduino1.D10, R4.Pin_1, R12.Pin_1
  N6: Arduino1.D7, R5.Pin_1, R13.Pin_1
  N7: Arduino1.D6, R6.Pin_1, R14.Pin_1
  N8: Arduino1.D5, R7.Pin_1, R15.Pin_1
  N9: Arduino1.D4, R8.Pin_1, R16.Pin_1
  N10: R1.Pin_0, LED9.anode
  N11: R2.Pin_0, LED10.anode
  N12: R3.Pin_0, LED11.anode
  N13: R4.Pin_0, LED12.anode
  N14: R5.Pin_0, LED13.anode
  N15: R6.Pin_0, LED16.anode
  N16: R7.Pin_0, LED15.anode
  N17: R8.Pin_0, LED18.anode
  N18: R9.Pin_0, LED1.anode
  N19: R10.Pin_0, LED2.anode
  N20: R11.Pin_0, LED3.anode
  N21: R12.Pin_0, LED5.anode
  N22: R13.Pin_0, LED4.anode
  N23: R14.Pin_0, LED8.anode
  N24: R15.Pin_0, LED7.anode
  N25: R16.Pin_0, LED17.anode
