# Fritzing sketch id4200_Sketch_TLC5940NT_0 (saved by Fritzing 0.8.5b)
breadboards: 1

parts:
  U2 = TLC5940NT
  Bauteil1 = Arduino Uno (Rev3)
  R1 = Resistor [tolerance=±5% resistance=2.2k package=THT]
  R2 = Resistor [tolerance=±5% resistance=3.3k package=THT]
  C1 = Tantalum Capacitor [capacitance=0.1µF package="100 mil [THT, tantalum]"]
  J1 = Basic Servo

nets:
  N1: U2.connector0, R2.Pin_1, J1.pulse
  N2: U2.connector17, Bauteil1.D3_PWM
  N3: U2.connector19, R1.Pin_0
  5V: U2.connector20, Bauteil1.5V, R2.Pin_0, C1.+, J1.vcc
  GND: U2.connector21, U2.connector26, Bauteil1.GND, R1.Pin_1, C1.-, J1.gnd
  N4: U2.connector22, Bauteil1.D10_PWM/SS
  N5: U2.connector23, Bauteil1.D9_PWM
  N6: U2.connector24, Bauteil1.D13/SCK
  N7: U2.connector25, Bauteil1.D11_PWM/MOSI
