# Fritzing sketch id4201_TMB_Diagrama_2_0 (saved by Fritzing 0.9.3b)

parts:
  A_MEga = Arduino Mega 2560 (Rev3)
  SEN1 = Pulse_Sensor
  SEN2 = Pulse_Sensor
  LED1 = LED - 5mm [color="Red (633nm)" package="5 mm [THT]"]
  U2 = 74HC595 [package="DIP16 [THT]"]
  DI1 = 7-Segment LED Display [package=THT]
  U3 = 74HC595 [package="DIP16 [THT]"]
  DI2 = 7-Segment LED Display [package=THT]
  U4 = 74HC595 [package="DIP16 [THT]"]
  DI3 = 7-Segment LED Display [package=THT]
  U5 = 74HC595 [package="DIP16 [THT]"]
  U6 = 74HC595 [package="DIP16 [THT]"]
  DI4 = 7-Segment LED Display [package=THT]
  DI5 = 7-Segment LED Display [package=THT]
  BTn_2 = Pushbutton [package="[THT]"]
  BTn1 = Pushbutton [package="[THT]"]
  Indutivo_1 = IC, SIP package, 3 pins [chip_label=IND]
  5V = Battery
  Indutivo_2 = IC, SIP package, 3 pins [chip_label=IND]
  Indutivo_3 = IC, SIP package, 3 pins [chip_label=IND]
  Indutivo_4 = IC, SIP package, 3 pins [chip_label=IND]
  CONV_DC = IC, SIP package, 3 pins [chip_label="Voltage Regulator 12V"]
  BTn_3 = Pushbutton [package="[THT]"]
  CONV_DC1 = IC, SIP package, 3 pins [chip_label="Voltage Regulator 7V"]
  R1 = Resistor [tolerance=±5% resistance=220 package=THT]  # not connected
  R2 = Resistor [tolerance=±5% resistance=220 package=THT]  # not connected
  R3 = Resistor [tolerance=±5% resistance=220 package=THT]  # not connected
  R4 = Resistor [tolerance=±5% resistance=220 package=THT]  # not connected
  LoRA = IC, SIP package, 6 pins [chip_label=LoRA]  # not connected

nets:
  N1: A_MEga.A0, SEN1.connector2
  N2: A_MEga.A1, SEN2.connector2
  GND: A_MEga.GND, SEN1.connector1, SEN2.connector1, LED1.cathode, U2.Q5, U2.GND, U3.Q5, U3.GND, U4.Q5, U4.GND, U5.Q5, U5.GND, U6.Q5, U6.GND, 5V.+, Indutivo_4.pin1, CONV_DC.pin2, CONV_DC1.pin2
  N3: A_MEga.D13_PWM, BTn1.Pin_3
  N4: A_MEga.D12_PWM, BTn_2.Pin_3, BTn_2.Pin_4
  N5: A_MEga.D11_PWM, BTn_3.Pin_3, BTn_3.Pin_4
  VCC: A_MEga.5V, SEN1.connector0, SEN2.connector0, U2.Q3, U2.Q4, U2.VCC, U3.Q3, U3.Q4, U3.VCC, U4.Q3, U4.Q4, U4.VCC, U5.Q3, U5.Q4, U5.VCC, U6.Q3, U6.Q4, U6.VCC, BTn_2.Pin_1, BTn_2.Pin_2, BTn1.Pin_1, 5V.-, CONV_DC.pin1, BTn_3.Pin_1, CONV_DC1.pin1
  N6: A_MEga.D22, U6.Q7
  N7: A_MEga.D23, U6.Q1
  N8: A_MEga.D24, U6.Q2
  N9: A_MEga.D25, U6.Q6
  N10: A_MEga.D26, U3.Q7
  N11: A_MEga.D27, U3.Q1
  N12: A_MEga.D28, U3.Q2
  N13: A_MEga.D29, U3.Q6
  N14: A_MEga.D30, U2.Q7
  N15: A_MEga.D31, U2.Q1
  N16: A_MEga.D32, U2.Q2
  N17: A_MEga.D33, U2.Q6
  N18: A_MEga.D34, U4.Q7
  N19: A_MEga.D35, U4.Q1
  N20: A_MEga.D36, U4.Q2
  N21: A_MEga.D37, U4.Q6
  N22: A_MEga.D38, U5.Q7
  N23: A_MEga.D39, U5.Q1
  N24: A_MEga.D40, U5.Q2
  N25: A_MEga.D41, U5.Q6
  N26: A_MEga.D42, Indutivo_4.pin3
  N27: A_MEga.D43, Indutivo_3.pin3
  N28: A_MEga.D44, Indutivo_2.pin3
  N29: A_MEga.D45, Indutivo_1.pin3
  N30: A_MEga.D51, LED1.anode
  N31: U2.Q7', DI1.cathodeE
  N32: U2.MR, DI1.cathodeD
  N33: U2.SH_CP, DI1.cathodeC
  N34: U2.ST_CP, DI1.cathodeB
  N35: U2.OE, DI1.cathodeA
  N36: U2.DS, DI1.cathodeG
  N37: U2.Q0, DI1.cathodeF
  N38: DI1.commAnode, DI2.commAnode, DI3.commAnode, DI4.commAnode, DI5.commAnode, CONV_DC1.pin3
  N39: U3.Q7', DI2.cathodeE
  N40: U3.MR, DI2.cathodeD
  N41: U3.SH_CP, DI2.cathodeC
  N42: U3.ST_CP, DI2.cathodeB
  N43: U3.OE, DI2.cathodeA
  N44: U3.DS, DI2.cathodeG
  N45: U3.Q0, DI2.cathodeF
  N46: U4.Q7', DI3.cathodeE
  N47: U4.MR, DI3.cathodeD
  N48: U4.SH_CP, DI3.cathodeC
  N49: U4.ST_CP, DI3.cathodeB
  N50: U4.OE, DI3.cathodeA
  N51: U4.DS, DI3.cathodeG
  N52: U4.Q0, DI3.cathodeF
  N53: U5.Q7', DI4.cathodeE
  N54: U5.MR, DI4.cathodeD
  N55: U5.SH_CP, DI4.cathodeC
  N56: U5.ST_CP, DI4.cathodeB
  N57: U5.OE, DI4.cathodeA
  N58: U5.DS, DI4.cathodeG
  N59: U5.Q0, DI4.cathodeF
  N60: U6.Q7', DI5.cathodeE
  N61: U6.MR, DI5.cathodeD
  N62: U6.SH_CP, DI5.cathodeC
  N63: U6.ST_CP, DI5.cathodeB
  N64: U6.OE, DI5.cathodeA
  N65: U6.DS, DI5.cathodeG
  N66: U6.Q0, DI5.cathodeF
  N67: Indutivo_1.pin1, Indutivo_2.pin1, Indutivo_3.pin1
  N68: Indutivo_1.pin2, Indutivo_2.pin2, Indutivo_3.pin2, Indutivo_4.pin2, CONV_DC.pin3
