# Fritzing sketch id4202_FirstSketch_0 (saved by Fritzing 0.9.1b)
breadboards: 1

parts:
  Part1 = Arduino Uno (Rev3)
  U1 = AD5206 Digital Potentiometer [maximum_resistance=10kΩ package="DIP28 [THT]"]  # not connected
  R1 = Resistor [tolerance=±5% resistance=220 package=THT]  # not connected
  R2 = Resistor [tolerance=±5% resistance=220 package=THT]  # not connected
  R3 = Resistor [tolerance=±5% resistance=220 package=THT]  # not connected
  R4 = Resistor [tolerance=±5% resistance=10k package=THT]  # not connected
  R5 = Resistor [tolerance=±5% resistance=10k package=THT]  # not connected
  R6 = Resistor [tolerance=±5% resistance=10k package=THT]  # not connected
  Part2 = Thumb Joystick

nets:
  N1: Part1.D10_PWM/SS, Part2.SEL
  N2: Part1.D11_PWM/MOSI, Part2.HORZ
  N3: Part1.D12/MISO, Part2.VERT
  5V: Part1.5V, Part2.VCC
  GND: Part1.GND, Part2.GND
