# Fritzing sketch id4204_TMP36_0 (saved by Fritzing 0.8.6b)
circuit board: 2.81638cm x 3.84764cm
breadboards: 1

parts:
  U2 = TMP36 Temperature Sensor [package="TO92 [THT]"]
  C1 = Ceramic Capacitor [capacitance=100nF package="100 mil [THT, multilayer]"]
  U1 = SPARKCORE
  part = Ceramic Capacitor [capacitance=100nF package="100 mil [THT, multilayer]"]  # not connected

nets (from the pcb view):
  N1: U2.+Vs, U1.connector62
  N2: U2.Vout, C1.0, U1.connector48
  N3: U2.GND, C1.1, U1.connector51
