# Fritzing sketch id4205_tmp37_0 (saved by Fritzing 0.7.0b)
breadboards: 1

parts:
  J1 = female pin header, 3 pins [form="♀ (female)"]
  T1 = LM35 Temperature Sensor [package="TO92 [THT]"]

nets:
  N1: J1.pin1, T1.GND
  N2: J1.pin2, T1.Vout
  N3: J1.pin3, T1.+Vs

notes:
  TMP37
