# Fritzing sketch id4206_16x2_blu_TnH_0 (saved by Fritzing 0.9.3b)
breadboards: 1

parts:
  元件1 = Arduino Uno (Rev3)
  元件2 = LCD1602-I2C_
  元件3 = Bluetooth HC-05 Macho
  Part1 = KY-015

nets:
  N1: 元件1.A1, Part1.connector1
  N2: 元件1.A4/SDA, 元件2.connector2
  N3: 元件1.A5/SCL, 元件2.connector3
  N4: 元件1.D10_PWM/SS, 元件3.TXD
  N5: 元件1.D11_PWM/MOSI, 元件3.RXD
  N6: 元件1.3V3, Part1.connector2
  5V: 元件1.5V, 元件2.connector1, 元件3.VCC
  GND: 元件1.GND, 元件2.connector0, 元件3.GND, Part1.connector0
