# Fritzing sketch id4207_Toggle_LED_by_button_0 (saved by Fritzing 0.9.3b)
circuit board: 13.2428cm x 6.30458cm
breadboards: 1

parts:
  Arduino_Mega_2560 = Arduino Mega 2560 (Rev3)
  Rup = Resistor [tolerance=±5% resistance=10k package=THT]
  S1 = Pushbutton [package="[SMD]"]

nets:
  N1: Arduino_Mega_2560.5V, Rup.Pin_0
  N2: Arduino_Mega_2560.GND, S1.Pin_3, S1.Pin_4
  N3: Arduino_Mega_2560.D2_PWM, Rup.Pin_1, S1.Pin_1, S1.Pin_2

notes:
  Button toggles the internal LED on pin 13.
