# Fritzing sketch id4208_Untitled_Sketch_0 (saved by Fritzing 0.9.3b)
circuit board: 8.46667cm x 5.64444cm

parts:
  LCD1 = LCD screen
  R1 = Rotary Potentiometer (Small) [maximum_resistance=100kΩ package=THT]
  S1 = Pushbutton [package=THT]
  S2 = Toggle Switch [package=THT]
  S3 = Toggle Switch [package=THT]
  S4 = Toggle Switch [package=THT]
  S5 = Toggle Switch [package=THT]
  S6 = Toggle Switch [package=THT]
  S7 = Toggle Switch [package=THT]
  S8 = Toggle Switch [package=THT]
  S9 = Toggle Switch [package=THT]
  R2 = Resistor [tolerance=±5% resistance=220 package=THT]
  Power_plug1 = Power plug
  S10 = Toggle Switch [package=THT]
  C1 = Electrolytic Capacitor [capacitance=1µF package="100 mil [THT, electrolytic]"]

nets:
  VSS: LCD1.VSS, LCD1.R/W, LCD1.LED-, R1.leg2, S2.L2, S3.L2, S4.L2, S5.L2, S6.L2, S7.L2, S8.L2, S9.L2, R2.Pin_0, Power_plug1.GND, S10.L2
  VDD: LCD1.VDD, LCD1.LED+, R1.leg1, S1.leg0, S2.L1, S3.L1, S4.L1, S5.L1, S6.L1, S7.L1, S8.L1, S9.L1, Power_plug1.VCC, S10.L1, C1.+
  N1: LCD1.V0, R1.wiper
  N2: LCD1.RS, S10.COM
  N3: LCD1.E, S1.leg1, R2.Pin_1, C1.-
  N4: LCD1.DB0, S2.COM
  N5: LCD1.DB1, S6.COM
  N6: LCD1.DB2, S9.COM
  N7: LCD1.DB3, S5.COM
  N8: LCD1.DB4, S8.COM
  N9: LCD1.DB5, S7.COM
  N10: LCD1.DB6, S3.COM
  N11: LCD1.DB7, S4.COM
