# Fritzing sketch id4209_button_light_tone_0 (saved by Fritzing 0.9.3b)
breadboards: 1

parts:
  Part1 = Arduino Uno (Rev3)
  J1 = Piezo Speaker
  LED1 = LED - 5mm [color="Red (633nm)" package="5 mm [THT]"]
  S1 = Pushbutton [package="[THT]"]
  R1 = Resistor [tolerance=±5% resistance=220 package=THT]

nets:
  N1: Part1.D9_PWM, J1.pin2
  N2: Part1.D13/SCK, LED1.anode
  N3: Part1.GND, J1.pin1, LED1.cathode
  N4: Part1.D7, S1.Pin_3, S1.Pin_4, R1.Pin_1
  N5: Part1.5V, S1.Pin_1, S1.Pin_2
