# Fritzing sketch id4210_buzzerPotentiometerDisplayFrequency_0 (saved by Fritzing 0.9.3b)
breadboards: 1

parts:
  Part1 = Arduino Uno (Rev3)
  LCD1 = LCD screen
  R2 = Resistor [tolerance=±5% resistance=330 package=THT]
  R3 = Trimmer Potentiometer [maximum_resistance=10kΩ package=THT]
  R5 = Resistor [tolerance=±5% resistance=220 package=THT]
  SG2 = Buzzer 12mm [package=buzzer-12mm-ns]
  R6 = Rotary Potentiometer (Large) [maximum_resistance=100kΩ package=THT]

nets:
  N1: Part1.A0, R6.wiper
  N2: Part1.D11_PWM/MOSI, LCD1.E
  N3: Part1.D12/MISO, LCD1.RS
  N4: Part1.D2, LCD1.DB7
  N5: Part1.D3_PWM, LCD1.DB6
  N6: Part1.D4, LCD1.DB5
  N7: Part1.D5_PWM, LCD1.DB4
  N8: Part1.D7, R2.Pin_1
  N9: LCD1.VSS, LCD1.R/W, LCD1.LED-, R3.leg1, SG2.1, R6.leg2
  N10: LCD1.VDD, R3.leg2, R5.Pin_0, R6.leg1
  N11: LCD1.V0, R3.wiper
  N12: LCD1.LED+, R5.Pin_1
  N13: R2.Pin_0, SG2.2
