# Fritzing sketch id4211_proyecto1plhm_0 (saved by Fritzing 0.9.3b)
breadboards: 1

parts:
  R1 = Resistor [tolerance=±5% resistance=220 package=THT]
  R2 = Resistor [tolerance=±5% resistance=220 package=THT]
  J1 = Piezo Speaker
  LED2 = LED - 5mm [color="Red (660nm)" package="5 mm [THT]"]
  LED3 = LED - 5mm [color="Green (555nm)" package="5 mm [THT]"]
  Componente1 = Arduino Uno (Rev3)
  Wally = HC-SR04 ultrasonic distance sensor

nets:
  N1: R1.Pin_0, LED2.anode
  N2: R1.Pin_1, Componente1.D2
  N3: R2.Pin_0, LED3.anode
  N4: R2.Pin_1, Componente1.D7
  N5: J1.pin1, LED2.cathode, LED3.cathode, Componente1.GND, Wally.connector3
  N6: J1.pin2, Componente1.D6_PWM
  N7: Componente1.D10_PWM/SS, Wally.connector2
  N8: Componente1.D11_PWM/MOSI, Wally.connector1
  N9: Componente1.5V, Wally.connector0
