# Fritzing sketch id4212_tophat_0 (saved by Fritzing 0.9.2b)
breadboards: 1

parts:
  Teensy_LC = Teensy 3.0
  joystick_(Parallax) = Thumb Joystick
  LED1 = RGB LED (com. cathode, rgb) [package="5 mm [THT]"]
  J1 = Piezo Speaker
  S3 = Pushbutton [package="[THT]"]
  S2 = Pushbutton [package="[THT]"]
  S1 = Pushbutton [package="[THT]"]
  R3 = Resistor [tolerance=±5% resistance=220 package=THT]
  R2 = Resistor [tolerance=±5% resistance=220 package=THT]
  R1 = Resistor [tolerance=±5% resistance=220 package=THT]
  R4 = Resistor [tolerance=±5% resistance=220 package=THT]
  R5 = Resistor [tolerance=±5% resistance=220 package=THT]

nets:
  N1: Teensy_LC.GND, J1.pin1, R3.Pin_1, R2.Pin_1, R1.Pin_1
  N2: Teensy_LC.A1/D15, R5.Pin_0
  N3: Teensy_LC.A2/D16, R4.Pin_0
  N4: joystick_(Parallax).VERT, joystick_(Parallax).VCC
  N5: LED1.green_anode, R4.Pin_1
  N6: LED1.blue_anode, R5.Pin_1
  N7: S3.Pin_1, S3.Pin_2, R3.Pin_0
  N8: S3.Pin_3, S3.Pin_4, S2.Pin_3, S2.Pin_4, S1.Pin_3, S1.Pin_4
  N9: S2.Pin_1, S2.Pin_2, R2.Pin_0
  N10: S1.Pin_1, S1.Pin_2, R1.Pin_0
