# Fritzing sketch id4213_YIC_PROJECT_0 (saved by Fritzing 0.9.3b)
breadboards: 2

parts:
  LCD1 = LCD screen
  R1 = Rotary Potentiometer (Small) [maximum_resistance=100kΩ package=THT]
  Part1 = Arduino Uno (Rev3)
  Part2 = Gas Sensor Breakout Board
  U1 = G3VM-61E1 [package=g3vm-61e1]
  T1 = LM35 Temperature Sensor [package="TO92 [THT]"]
  M1 = DC Motor

nets:
  GND: LCD1.VSS, LCD1.R/W, LCD1.LED-, R1.leg2, Part1.GND, Part2.GND, U1.P$5, T1.GND, M1.pin_1
  VDD: LCD1.VDD, LCD1.LED+, R1.leg1, Part1.5V, Part2.A1, U1.P$2, U1.P$6, T1.+Vs
  N1: LCD1.V0, R1.wiper
  N2: LCD1.RS, Part1.D12/MISO
  N3: LCD1.E, Part1.D11_PWM/MOSI
  N4: LCD1.DB4, Part1.D5_PWM
  N5: LCD1.DB5, Part1.D4
  N6: LCD1.DB6, Part1.D3_PWM
  N7: LCD1.DB7, Part1.D9_PWM
  N8: Part1.A0, T1.Vout
  N9: Part1.A1, Part2.B1
  N10: Part1.D7, U1.P$4
  N11: U1.P$3, M1.pin_2
