# Fritzing sketch id4214_Toster_0 (saved by Fritzing 0.9.3b)
breadboards: 1

parts:
  Componente1 = Arduino Uno (Rev3)
  LCD1 = LCD screen
  S1 = Square Pushbutton
  LED1 = smd LED [color="Red (633nm)" package="0603 [SMD]"]
  R1 = Resistor [tolerance=±5% resistance=220 package=THT]
  Matrix_keypad1 = CMG
  KY-1 = keyes
  KY-2 = keyes
  KY-3 = keyes
  KY-4 = keyes

nets:
  N1: Componente1.A0, Matrix_keypad1.connector25
  N2: Componente1.A1, Matrix_keypad1.connector31
  N3: Componente1.A2, Matrix_keypad1.connector30
  N4: Componente1.A3, Matrix_keypad1.connector29
  N5: Componente1.D8, LCD1.E
  N6: Componente1.D9_PWM, KY-3.connector1
  N7: Componente1.D10_PWM/SS, KY-1.connector1
  N8: Componente1.D11_PWM/MOSI, KY-2.connector1
  N9: Componente1.D12/MISO, LCD1.RS
  N10: Componente1.D13/SCK, KY-4.connector1
  N11: Componente1.D2, LCD1.DB7
  N12: Componente1.D3_PWM, LCD1.DB6
  N13: Componente1.D4, LCD1.DB5
  N14: Componente1.D5_PWM, LCD1.DB4
  N15: Componente1.D6_PWM, R1.Pin_0
  N16: Componente1.D7, S1.leg0
  5V: Componente1.5V, LCD1.VDD, LCD1.LED+, S1.leg1, KY-1.connector0, KY-2.connector0, KY-3.connector0, KY-4.connector0
  GND: Componente1.GND, LCD1.VSS, LCD1.V0, LCD1.R/W, LCD1.LED-, LED1.anode, KY-1.connector2, KY-2.connector2, KY-3.connector2, KY-4.connector2
  N17: LED1.cathode, R1.Pin_1
  N18: KY-1.connector4, KY-1.connector5, KY-2.connector3, KY-2.connector4, KY-2.connector5, KY-3.connector4, KY-3.connector5, KY-4.connector3, KY-4.connector5
