# Fritzing sketch id4215_Touch_My_Piano_0 (saved by Fritzing 0.8.3b)
circuit board: 6.18296cm x 5.43304cm
breadboards: 1

parts:
  IC1 = General purpose bipolar Timer [package=dil-08]
  BAT1 = Battery Holders [package=battcon_20mm]
  S1 = Toggle Switch [package=THT]
  R2 = Resistor [tolerance=±5% resistance=20M package=THT]
  SG1 = Buzzer 12mm [package=buzzer-12mm]
  R3 = Resistor [tolerance=±5% resistance=300k package=THT]
  R4 = Resistor [tolerance=±5% resistance=10k package=THT]
  R5 = Resistor [tolerance=±5% resistance=10k package=THT]
  R6 = Resistor [tolerance=±5% resistance=10k package=THT]
  R7 = Resistor [tolerance=±5% resistance=10k package=THT]
  R8 = Resistor [tolerance=±5% resistance=10k package=THT]
  R9 = Resistor [tolerance=±5% resistance=10k package=THT]
  R10 = Resistor [tolerance=±5% resistance=10k package=THT]
  R11 = Resistor [tolerance=±5% resistance=10k package=THT]
  LED1 = LED - 5mm [color="Blue (470nm)" package="5 mm [THT]"]
  J4 = female pin header, 1 pin [form="♀ (female)"]
  J1 = female pin header, 1 pin [form="♀ (female)"]
  J3 = female pin header, 1 pin [form="♀ (female)"]
  J5 = female pin header, 1 pin [form="♀ (female)"]
  J6 = female pin header, 1 pin [form="♀ (female)"]
  J7 = female pin header, 1 pin [form="♀ (female)"]
  J9 = female pin header, 1 pin [form="♀ (female)"]
  J10 = female pin header, 1 pin [form="♀ (female)"]
  C2_-_680pF = Capacitor [package=cap-pth-small-kit]
  J8 = female pin header, 1 pin [form="♀ (female)"]
  C1_-_0_1µF = Capacitor [package=cap-pth-small-kit]
  Pad1 = Pad [width=14.4874074074074 height=11.8533333333333 connect=center]
  Pad2 = Pad [width=6.20888888888889 height=8.09037037037036 connect=center]
  Pad3 = Pad [width=6.20888888888889 height=8.09037037037036 connect=center]
  Pad4 = Pad [width=6.20888888888889 height=8.09037037037036 connect=center]
  Pad5 = Pad [width=6.20888888888889 height=8.09037037037036 connect=center]
  Pad6 = Pad [width=6.20888888888889 height=8.09037037037036 connect=center]
  Pad7 = Pad [width=6.20888888888889 height=8.09037037037036 connect=center]
  Pad8 = Pad [width=6.20888888888889 height=8.09037037037036 connect=center]
  Pad9 = Pad [width=6.20888888888889 height=8.09037037037036 connect=center]

nets:
  GND: IC1.GND, BAT1.-, R2.Pin_1, SG1.2, LED1.cathode, C2_-_680pF.2, C1_-_0_1µF.2
  N1: IC1.TRI, IC1.TRE, R2.Pin_0, R3.Pin_1, C2_-_680pF.1
  N2: IC1.OUT, SG1.1
  3V: IC1._RES, IC1.VCC+, S1.L2, R4.Pin_0, LED1.anode
  N3: IC1.CON, C1_-_0_1µF.1
  N4: IC1.DIS, R4.Pin_1, R5.Pin_0, J3.pin1, Pad2.pad
  N5: BAT1.+, S1.COM
  N6: R3.Pin_0, J1.pin1, Pad1.pad
  N7: R5.Pin_1, R6.Pin_0, J4.pin1, Pad3.pad
  N8: R6.Pin_1, R7.Pin_0, J5.pin1, Pad4.pad
  N9: R7.Pin_1, R8.Pin_0, J6.pin1, Pad5.pad
  N10: R8.Pin_1, R9.Pin_0, J7.pin1, Pad6.pad
  N11: R9.Pin_1, R10.Pin_0, J8.pin1, Pad7.pad
  N12: R10.Pin_1, R11.Pin_0, J9.pin1, Pad8.pad
  N13: R11.Pin_1, J10.pin1, Pad9.pad

notes:
  TOUCH MY
  PIANO
  C1
  C2
  Designed by Zack Freedman
  of Voidstar Lab
  zackfreedman.com/projects/touchmypiano
  Based on Drawdio
  by Jay Silver
  ☜
  Touch My Piano - Fritzing Contest Entry
  Designed by Zack Freedman of Voidstar Lab
  http://zackfreedman.com/projects/touchmypiano
  Based on Drawdio by Jay Silver
  Touch My Piano
