# Fritzing sketch id4216_touch_sensor_with_pincode_0 (saved by Fritzing 0.9.3b)
breadboards: 1

parts:
  Part1 = Arduino Uno (Rev3)
  LCD1 = LCD screen
  R1 = Resistor [tolerance=±5% resistance=220 package=THT]
  R2 = Resistor [tolerance=±5% resistance=1M package=THT]
  S1 = Pushbutton [package="[THT]"]
  S2 = Pushbutton [package="[THT]"]
  S3 = Pushbutton [package="[THT]"]
  S4 = Pushbutton [package="[THT]"]
  R3 = Resistor [tolerance=±5% resistance=1M package=THT]
  R4 = Resistor [tolerance=±5% resistance=1M package=THT]
  R5 = Resistor [tolerance=±5% resistance=1M package=THT]
  R6 = Resistor [tolerance=±5% resistance=10M package=THT]
  R7 = Resistor [tolerance=±5% resistance=1M package=THT]

nets:
  N1: Part1.A0, S1.Pin_1, S1.Pin_2, S2.Pin_1, S2.Pin_2, S3.Pin_1, S3.Pin_2, S4.Pin_1, S4.Pin_2, R6.Pin_1
  N2: Part1.D11_PWM/MOSI, LCD1.E
  N3: Part1.D12/MISO, LCD1.RS
  N4: Part1.D2, LCD1.DB7
  N5: Part1.D3_PWM, LCD1.DB6
  N6: Part1.D4, LCD1.DB5
  N7: Part1.D5_PWM, LCD1.DB4
  N8: Part1.D6_PWM, R2.Pin_1
  N9: Part1.D7, R2.Pin_0
  5V: Part1.5V, LCD1.VDD, R1.Pin_0, R7.Pin_0
  GND: Part1.GND, LCD1.VSS, LCD1.V0, LCD1.R/W, LCD1.LED-, R6.Pin_0
  N10: LCD1.LED+, R1.Pin_1
  N11: S1.Pin_3, S1.Pin_4, R3.Pin_1
  N12: S2.Pin_3, S2.Pin_4, R3.Pin_0, R4.Pin_1
  N13: S3.Pin_3, S3.Pin_4, R4.Pin_0, R5.Pin_1
  N14: S4.Pin_3, S4.Pin_4, R5.Pin_0, R7.Pin_1

notes:
  Metal Foil
