# Fritzing sketch id4218_speed_trap_0 (saved by Fritzing 0.9.3b)
breadboards: 1

parts:
  U1 = LCD-16X2 [package=lcd-16x2]
  R1 = Rotary Potentiometer (Small) [maximum_resistance=100kΩ package=THT]
  Part1 = Arduino Mega 2560 (Rev3)
  R3 = Resistor [tolerance=±5% resistance=220 package=THT]
  R4 = Resistor [tolerance=±5% resistance=220 package=THT]
  R5 = Resistor [tolerance=±5% resistance=10k package=THT]
  R6 = Photocell (LDR) [package=THT]
  R7 = Resistor [tolerance=±5% resistance=10k package=THT]
  R8 = Photocell (LDR) [package=THT]  # not connected
  LED1 = LED - 5mm [color="Red (633nm)" package="5 mm [THT]"]
  LED2 = LED - 5mm [color="Red (633nm)" package="5 mm [THT]"]

nets:
  VSS: U1.VSS, U1.R_W, U1.K, R1.leg2, Part1.GND, R5.Pin_0, R7.Pin_0, LED1.cathode, LED2.cathode
  VDD: U1.VDD, U1.A, R1.leg1, Part1.5V, R6.pin_1
  N1: U1.VO, R1.wiper
  N2: U1.RS, Part1.D12_PWM
  N3: U1.E, Part1.D11_PWM
  N4: U1.DB4, Part1.D5_PWM
  N5: U1.DB5, Part1.D4_PWM
  N6: U1.DB6, Part1.D3_PWM
  N7: U1.DB7, Part1.D2_PWM
  N8: Part1.A0, R5.Pin_1, R6.pin_0
  N9: Part1.A1, R7.Pin_1
  N10: Part1.D7_PWM, R3.Pin_0, R4.Pin_1
  N11: R3.Pin_1, LED1.anode
  N12: R4.Pin_0, LED2.anode
