# Fritzing sketch id4219_sis_0 (saved by Fritzing 0.9.3b)
breadboards: 1

parts:
  R1 = Resistor [tolerance=±5% resistance=220 package=THT]
  R2 = Resistor [tolerance=±5% resistance=220 package=THT]
  R3 = Resistor [tolerance=±5% resistance=220 package=THT]
  Componente1 = Arduino Uno (Rev3)
  T1 = LM35 Temperature Sensor [package="TO92 [THT]"]
  LED1 = LED - 5mm [color="Yellow (595nm)" package="5 mm [THT]"]
  LED3 = LED - 5mm [color="Red (633nm)" package="5 mm [THT]"]
  7_Segment2 = 7-Segment LED Display [package=THT]
  7_Segment1 = 7-Segment LED Display [package=THT]
  LED2 = smd LED [color="Green (555nm)" package="0603 [SMD]"]

nets:
  N1: R1.Pin_0, LED1.anode
  GND: R1.Pin_1, R2.Pin_1, R3.Pin_1, Componente1.GND, T1.GND
  N2: R2.Pin_0, LED3.anode
  N3: R3.Pin_0, LED2.anode
  N4: Componente1.A0, T1.Vout
  N5: Componente1.A1, 7_Segment2.cathodeDP
  N6: Componente1.D8, 7_Segment1.commAnode#2
  N7: Componente1.D9_PWM, LED2.cathode
  N8: Componente1.D10_PWM/SS, LED1.cathode
  N9: Componente1.D11_PWM/MOSI, LED3.cathode
  N10: Componente1.D12/MISO, 7_Segment1.cathodeG
  N11: Componente1.D13/SCK, 7_Segment1.cathodeF
  N12: Componente1.D2, 7_Segment2.cathodeB
  N13: Componente1.D3_PWM, 7_Segment2.cathodeA
  N14: Componente1.D4, 7_Segment2.cathodeC
  N15: Componente1.D5_PWM, 7_Segment1.cathodeD
  N16: Componente1.D6_PWM, 7_Segment1.cathodeE
  N17: Componente1.D7, 7_Segment1.commAnode#7
  N18: Componente1.5V, T1.+Vs
