# Fritzing sketch id421_BrainWave_0 (saved by Fritzing 0.7.4b)
breadboards: 1

parts:
  Bluetooth_Modem_-_BlueSMiRF_Gold1 = Bluetooth_Modem___BlueSMiRF_Gold [part_number=WRL-10268]
  Arduino1 = Arduino
  LED4 = RGB LED (com. anode, rbg) [package="5 mm [THT]"]
  R1 = Resistor [tolerance=±5% resistance=180k package=THT]
  R2 = Resistor [tolerance=±5% resistance=100k package=THT]
  R3 = Resistor [tolerance=±5% resistance=100k package=THT]

nets:
  N1: Bluetooth_Modem_-_BlueSMiRF_Gold1.connector2, Arduino1.D7
  N2: Bluetooth_Modem_-_BlueSMiRF_Gold1.connector3, Arduino1.GND, LED4.common_anode
  N3: Bluetooth_Modem_-_BlueSMiRF_Gold1.connector4, Arduino1.D0RX
  N4: Bluetooth_Modem_-_BlueSMiRF_Gold1.connector5, Arduino1.D1TX
  N5: Arduino1.D11, R1.Pin_0
  N6: Arduino1.D10, R3.Pin_0
  N7: Arduino1.D9, R2.Pin_0
  N8: LED4.red_cathode, R1.Pin_1
  N9: LED4.blue_cathode, R3.Pin_1
  N10: LED4.green_cathode, R2.Pin_1

notes:
  White TX wire from Arduino to BlueSMiRF should only be used to program BlueSMiRF initially. Once it is setup, you do not need it anymore.
