# Fritzing sketch id4220_TP_IoT_0 (saved by Fritzing 0.9.2b)

parts:
  Part1 = Arduino Uno (Rev3)  # not connected
  Raspberry_Pi_B_rev1 = Raspberry Pi B rev1
  LED1 = LED - 5mm [color="Red (633nm)" package="5 mm [THT]"]
  Raspberry_Pi1 = Raspberry Pi 2  # not connected
  Grove1 = Grove Light Sensor  # not connected
  Grove2 = Grove Temperature Sensor  # not connected
  Grove3 = Grove Buzz  # not connected
  Grove4 = Grove Button  # not connected
  Part2 = Ambient Light Sensor (TEMT6000 Breakout Board)
  Grove5 = Grove Infrared Emitter  # not connected
  LED2 = LED - 5mm [color="Red (633nm)" package="5 mm [THT]"]  # not connected
  RHT1 = Humidity and Temperature Sensor RHT03

nets:
  VCC: Raspberry_Pi_B_rev1.3V3, Part2.VCC, RHT1.Vcc
  GND: Raspberry_Pi_B_rev1.GND, LED1.cathode, Part2.GND, RHT1.GND_2
  N1: Raspberry_Pi_B_rev1.GPIO_18, RHT1.Data-signal
  N2: Raspberry_Pi_B_rev1.GPIO_4, Part2.S
  N3: Raspberry_Pi_B_rev1.GPIO_25, LED1.anode

notes:
  Long Pin
  Long Leg
  Short Leg
  Short Pin
  Light Sensor
  Temperature Sensor
  LED
