# Fritzing sketch id4223_brilloLED_potenciometroMirian_0 (saved by Fritzing 0.7.5b)
breadboards: 1

parts:
  LED1 = LED - 5mm [color="Red (633nm)" package="5 mm [THT]"]
  R2 = Resistor [tolerance=±5% resistance=220 package=THT]
  Arduino1 = Arduino
  R3 = Rotary Potentiometer (Small) [maximum_resistance=100kΩ]

nets:
  N1: LED1.cathode, R2.Pin_0
  N2: R2.Pin_1, Arduino1.GND, R3.leg2
  N3: Arduino1.+5V, R3.leg1
  N4: Arduino1.A0, R3.wiper
