# Fritzing sketch id4224_encender_y_apagar_un_led_con_pulsador_0 (saved by Fritzing 0.9.2b)
breadboards: 1

parts:
  LED1 = LED - 5mm [color="Red (633nm)" package="5 mm [THT]"]
  R1 = Resistor [tolerance=±5% resistance=220 package=THT]
  S1 = Pushbutton [package="[THT]"]
  R2 = Resistor [tolerance=±5% resistance=220 package=THT]
  Parte1 = Arduino Uno (Rev3)

nets:
  N1: LED1.cathode, R1.Pin_0, Parte1.D10_PWM/SS
  N2: S1.Pin_1, S1.Pin_2, R2.Pin_0
  N3: S1.Pin_3, S1.Pin_4
