# Fritzing sketch id4228_trabalho_de_escola_0 (saved by Fritzing 0.9.0b)
breadboards: 1

parts:
  LED1 = LEDs [package=led10mm]
  LED2 = LEDs [package=led10mm]
  LED3 = LEDs [package=led10mm]
  LED4 = LEDs [package=led10mm]
  LED5 = LEDs [package=led10mm]
  LED6 = LEDs [package=led10mm]
  LED7 = LEDs [package=led10mm]
  LED8 = LEDs [package=led10mm]
  LED9 = LEDs [package=led10mm]
  S1 = Square Pushbutton
  S2 = Square Pushbutton
  S3 = Square Pushbutton
  S4 = Square Pushbutton
  S5 = Square Pushbutton
  S6 = Square Pushbutton
  S7 = Square Pushbutton
  S8 = Square Pushbutton
  S9 = Square Pushbutton
  BAT1 = BC9VPC [package=bc9vpc]

nets:
  N1: LED1.A, LED2.A, LED3.A, LED4.A, LED5.A, LED6.A, LED7.A, LED8.A, LED9.A, BAT1.V-
  N2: LED1.C, S8.leg1
  N3: LED2.C, S7.leg1
  N4: LED4.C, S5.leg1
  N5: LED5.C, S4.leg1
  N6: LED6.C, S3.leg1
  N7: LED7.C, S2.leg1
  N8: LED8.C, S1.leg1
  N9: LED9.C, S9.leg1
  N10: S1.leg0, S2.leg0, S3.leg0, S4.leg0, S5.leg0, S6.leg0, S7.leg0, S8.leg0, S9.leg0, BAT1.V+
