# Fritzing sketch id4229_arduino_button_selection_0 (saved by Fritzing 0.9.3b)
breadboards: 1

parts:
  R1 = Resistor [tolerance=±5% resistance=330 package=THT]
  R2 = Resistor [tolerance=±5% resistance=330 package=THT]
  R3 = Resistor [tolerance=±5% resistance=330 package=THT]
  LED1 = RGB LED (com. cathode, rbg) [package="5 mm [THT]"]
  S2 = Pushbutton [package=THT]
  S3 = Pushbutton [package=THT]
  S4 = Pushbutton [package=THT]
  R4 = Resistor [tolerance=±5% resistance=10k package=THT]
  R5 = Resistor [tolerance=±5% resistance=10k package=THT]
  R6 = Resistor [tolerance=±5% resistance=10k package=THT]
  Part1 = Arduino Mega 2560 (Rev3)

nets:
  N1: R1.Pin_0, Part1.D11_PWM
  N2: R1.Pin_1, LED1.red_anode
  N3: R2.Pin_0, Part1.D12_PWM
  N4: R2.Pin_1, LED1.blue_anode
  N5: R3.Pin_0, Part1.D13_PWM
  N6: R3.Pin_1, LED1.green_anode
  N7: LED1.common_cathode, R4.Pin_1, R5.Pin_1, R6.Pin_1, Part1.GND
  N8: S2.leg0, R6.Pin_0, Part1.D4_PWM
  N9: S2.leg1, S3.leg1, S4.leg1, Part1.5V
  N10: S3.leg0, R5.Pin_0, Part1.D3_PWM
  N11: S4.leg0, R4.Pin_0, Part1.D2_PWM

notes:
  STOP FORWARD REVERSE
  Red Green Blue
