# Fritzing sketch id422_V1_0 (saved by Fritzing 0.7.7b)
breadboards: 1

parts:
  Arduino1 = Arduino
  J1 = Basic Servo
  J2 = Basic Servo
  VENTILATOR_1 = DC Motor
  VENTILATOR_2 = DC Motor
  Part1 = Bluetooth Module Breakout - Roving Networks (RN-41)
  ULTRASONIC = Infrared Proximity Sensor

nets:
  N1: Arduino1.D2, ULTRASONIC.Vout
  N2: Arduino1.D1TX, Part1.UARTTX
  N3: Arduino1.D0RX, Part1.UARTRX
  3V3: Arduino1.3V3, Part1.VCC
  VCC: Arduino1.+5V, J1.vcc, J2.vcc, ULTRASONIC.Vcc
  GND: Arduino1.GND, J1.gnd, J2.gnd, VENTILATOR_1.pin_1, VENTILATOR_2.pin_1, Part1.GND, ULTRASONIC.GND
  N4: Arduino1.A0, J1.pulse
  N5: Arduino1.A1, J2.pulse
  N6: Arduino1.A2, VENTILATOR_1.pin_2
  N7: Arduino1.A3, VENTILATOR_2.pin_2
