# Fritzing sketch id4230_GY_NEO6MV2_0 (saved by Fritzing 0.9.3b)
breadboards: 1

parts:
  Bauteil1 = Arduino Uno (Rev3)
  GY-NEO6MV2 = SUP500F [package=sup500f]
  SIM800L_BO1 = SIM800L BO [part_number=SIM800L]

nets:
  N1: Bauteil1.D9_PWM, SIM800L_BO1.connector4
  N2: Bauteil1.D10_PWM/SS, SIM800L_BO1.connector5
  N3: Bauteil1.D3_PWM, GY-NEO6MV2.VCC
  N4: Bauteil1.D4, GY-NEO6MV2.GND
  N5: Bauteil1.ioref, GY-NEO6MV2.TX-O
  N6: Bauteil1.GND, GY-NEO6MV2.RX-I, SIM800L_BO1.connector6

notes:
  GND: Black
  VCC: Red + IOREF
  RX: Yellow
  TX: Green
  GND: Black
  VCC: Red
  RX: Yellow
  TX: Green
