# Fritzing sketch id4231_Traffic_Light_v_2.0_0 (saved by Fritzing 0.9.3b)
circuit board: 6.10392cm x 5.10413cm
breadboards: 1

parts:
  555/1 = 555 Timer [package="DIP8 [THT]"]
  555/2 = 555 Timer [package="DIP8 [THT]"]
  220 = Resistor [tolerance=±5% resistance=470 package=THT]
  470 = Resistor [tolerance=±5% resistance=220 package=THT]
  220_2 = Resistor [tolerance=±5% resistance=220 package=THT]
  10uF-100uF = Electrolytic Capacitor [capacitance=10µF package="100 mil [THT, electrolytic]"]
  10uF-100uF_2 = Electrolytic Capacitor [capacitance=1µF package="100 mil [THT, electrolytic]"]
  Red = LED - 5mm [color="Red (633nm)" package="5 mm [THT]"]
  Yellow = LED - 5mm [color="Yellow (595nm)" package="5 mm [THT]"]
  Green = LED - 5mm [color="Green (570nm)" package="5 mm [THT]"]
  VCC = Input Pins [form="♀ (female)"]
  100K = Input Pins [form="♀ (female)"]
  47K = Input Pins [form="♀ (female)"]

nets:
  N1: 555/1.Ground, 555/2.Ground, 10uF-100uF.-, 10uF-100uF_2.-, Green.cathode, VCC.connector1
  N2: 555/1.Trigger, 555/1.Threshold, 10uF-100uF_2.+, 100K.connector1
  N3: 555/1.Output, 555/2.Vcc_Supply_Voltage, Red.cathode, 100K.connector0
  N4: 555/1.Reset, 555/1.Vcc_Supply_Voltage, 555/2.Reset, 220.Pin_1, 470.Pin_1, VCC.connector0
  N5: 555/2.Trigger, 555/2.Threshold, 10uF-100uF.+, 47K.connector1
  N6: 555/2.Output, 220_2.Pin_1, 47K.connector0
  N7: 555/2.Discharge, Yellow.cathode
  N8: 220.Pin_0, Yellow.anode
  N9: 470.Pin_0, Red.anode
  N10: 220_2.Pin_0, Green.anode

notes:
  -
  +
  WaTco Designs
  V 2.8.18
