# Fritzing sketch id4232_traffic_light_project_0 (saved by Fritzing 0.9.3b)
breadboards: 2

parts:
  Part1 = Arduino Uno (Rev3)
  S1 = Pushbutton [package="[THT]"]
  R2 = Resistor [tolerance=±5% resistance=220 package="0402 [SMD]"]
  R3 = Resistor [tolerance=±5% resistance=220 package="0402 [SMD]"]
  R4 = Resistor [tolerance=±5% resistance=220 package="0402 [SMD]"]
  R5 = Resistor [tolerance=±5% resistance=220 package="0402 [SMD]"]
  R6 = Resistor [tolerance=±5% resistance=220 package="0402 [SMD]"]
  R7 = Resistor [tolerance=±5% resistance=220 package="0402 [SMD]"]
  R8 = Resistor [tolerance=±5% resistance=220 package="0402 [SMD]"]
  R9 = Resistor [tolerance=±5% resistance=220 package="0402 [SMD]"]
  LED1 = smd LED [color="Red (633nm)" package="0805 [SMD]"]
  LED2 = smd LED [color="Red (633nm)" package="0805 [SMD]"]
  LED3 = smd LED [color="Red (633nm)" package="0805 [SMD]"]
  LED4 = smd LED [color="Red (633nm)" package="0805 [SMD]"]
  LED5 = smd LED [color="Red (633nm)" package="0805 [SMD]"]
  LED6 = smd LED [color="Yellow (595nm)" package="0805 [SMD]"]
  LED7 = smd LED [color="Green (570nm)" package="0805 [SMD]"]
  S2 = Pushbutton [package="[THT]"]
  LED8 = smd LED [color="Red (633nm)" package="0805 [SMD]"]
  LED9 = smd LED [color="Red (633nm)" package="0805 [SMD]"]
  LED10 = smd LED [color="Red (633nm)" package="0805 [SMD]"]
  LED11 = smd LED [color="Red (633nm)" package="0805 [SMD]"]
  R10 = Resistor [tolerance=±5% resistance=220 package=THT]
  R11 = Resistor [tolerance=±5% resistance=220 package=THT]
  R12 = Resistor [tolerance=±5% resistance=220 package=THT]
  R13 = Resistor [tolerance=±5% resistance=220 package=THT]
  R14 = Resistor [tolerance=±5% resistance=220 package=THT]
  LED12 = smd LED [color="Red (633nm)" package="0805 [SMD]"]
  LED13 = smd LED [color="Yellow (595nm)" package="0805 [SMD]"]
  LED14 = smd LED [color="Green (570nm)" package="0805 [SMD]"]
  M1 = Dagu DGServo 9g (Pan and tilt) [part_number=RS001B]

nets (from the schematic view):
  N1: Part1.D8, S2.Pin_3, S2.Pin_4, R10.Pin_0
  N2: Part1.D9_PWM, R14.Pin_1
  N3: Part1.D10_PWM/SS, R13.Pin_1
  N4: Part1.D11_PWM/MOSI, R12.Pin_0
  N5: Part1.D12/MISO, R11.Pin_1
  N6: Part1.D13/SCK, M1.pulse
  GND: Part1.GND, R2.Pin_0, R5.Pin_1, LED1.cathode, LED2.cathode, LED3.cathode, LED4.cathode, LED5.cathode, LED5.anode, LED6.cathode, LED7.cathode, LED8.cathode, LED9.cathode, LED10.cathode, LED11.cathode, R10.Pin_1, LED12.cathode, LED13.cathode, M1.gnd
  N7: Part1.D0/RX, S1.Pin_3, S1.Pin_4, R2.Pin_1
  N8: Part1.D1/TX, R6.Pin_1
  N9: Part1.D2, R7.Pin_1
  N10: Part1.D3_PWM, R8.Pin_1
  N11: Part1.D4, R9.Pin_0
  5V: Part1.5V, S1.Pin_1, S1.Pin_2, S2.Pin_1, S2.Pin_2, M1.vcc
  N12: R3.Pin_0, LED7.anode
  N13: R3.Pin_1, LED12.anode
  N14: R4.Pin_0, LED6.anode
  N15: R4.Pin_1, LED13.anode
  N16: R5.Pin_0, LED14.anode
  N17: R6.Pin_0, LED4.anode
  N18: R7.Pin_0, LED3.anode
  N19: R8.Pin_0, LED2.anode
  N20: R9.Pin_1, LED1.anode
  N21: LED8.anode, R14.Pin_0
  N22: LED9.anode, R13.Pin_0
  N23: LED10.anode, R12.Pin_1
  N24: LED11.anode, R11.Pin_0
