# Fritzing sketch id4233_Traffic_Light_0 (saved by Fritzing 0.9.0b)
breadboards: 1

parts:
  Part1 = Arduino Uno (Rev3)
  LED1 = LED - 5mm [color="Red (633nm)" package="5 mm [THT]"]
  LED2 = LED - 5mm [color="Orange (605nm)" package="5 mm [THT]"]
  LED3 = LED - 5mm [color="Green (555nm)" package="5 mm [THT]"]
  R1 = Resistor [tolerance=±5% resistance=220 package=THT]
  R2 = Resistor [tolerance=±5% resistance=220 package=THT]
  R3 = Resistor [tolerance=±5% resistance=220 package=THT]

nets:
  N1: Part1.D0/RX, LED3.cathode
  N2: Part1.D2, LED2.cathode
  N3: Part1.D4, LED1.cathode
  N4: Part1.GND, R1.Pin_0, R2.Pin_0, R3.Pin_0
  N5: LED1.anode, R2.Pin_1
  N6: LED2.anode, R1.Pin_1
  N7: LED3.anode, R3.Pin_1
