# Fritzing sketch id4234_Semaforo_wip_0 (saved by Fritzing 0.9.1b)
breadboards: 1

parts:
  Componente1 = Arduino Uno (Rev3)
  S1 = Pushbutton [package="[THT]"]
  R1 = Resistor [tolerance=±5% resistance=10k package=THT]
  R2 = Resistor [tolerance=±5% resistance=220 package=THT]
  R3 = Resistor [tolerance=±5% resistance=220 package=THT]
  LED1 = LED - 5mm [color="Red (633nm)" package="5 mm [THT]"]
  LED2 = LED - 5mm [color="Yellow (595nm)" package="5 mm [THT]"]
  R4 = Resistor [tolerance=±5% resistance=220 package=THT]
  LED3 = LED - 5mm [color="Green (560nm)" package="5 mm [THT]"]

nets:
  N1: Componente1.D9_PWM, Componente1.5V, S1.Pin_3, S1.Pin_4, R1.Pin_1
  N2: Componente1.D2, R4.Pin_0
  N3: Componente1.D3_PWM, R3.Pin_0
  N4: Componente1.D4, R2.Pin_0
  N5: Componente1.GND, R1.Pin_0, LED1.cathode, LED2.cathode, LED3.cathode
  N6: R2.Pin_1, LED1.anode
  N7: R3.Pin_1, LED2.anode
  N8: R4.Pin_1, LED3.anode
