# Fritzing sketch id4235_trafficlight_0 (saved by Fritzing 0.7.4b)
breadboards: 1

parts:
  LED1 = LED - 5mm [color="Red (633nm)" package="5 mm [THT]"]
  LED2 = LED - 5mm [color="Yellow (585nm)" package="5 mm [THT]"]
  Arduino1 = Arduino
  LED3 = LED - 5mm [color="Green (555nm)" package="5 mm [THT]"]
  LED4 = LED - 5mm [color="Red (633nm)" package="5 mm [THT]"]
  LED5 = LED - 5mm [color="Yellow (585nm)" package="5 mm [THT]"]
  LED6 = LED - 5mm [color="Green (555nm)" package="5 mm [THT]"]
  LED7 = LED - 5mm [color="Red (633nm)" package="5 mm [THT]"]
  SPKR1 = Loudspeaker
  S1 = Pushbutton [package="[THT]"]
  R1 = Resistor [tolerance=±5% resistance=2.2k package=THT]

nets:
  N1: LED1.cathode, LED2.cathode, Arduino1.GND, LED3.cathode, LED4.cathode, LED5.cathode, LED6.cathode, SPKR1.pin1, S1.Pin_3, S1.Pin_4, R1.Pin_0
  N2: LED1.anode, Arduino1.D12
  N3: LED2.anode, Arduino1.D11
  N4: Arduino1.D10, LED3.anode
  N5: Arduino1.D9, LED4.anode
  N6: Arduino1.D8, LED5.anode
  N7: Arduino1.D7, LED6.anode
  N8: Arduino1.D4, LED7.anode
  N9: Arduino1.D3, SPKR1.pin2
  N10: Arduino1.D2, S1.Pin_1, S1.Pin_2
  N11: LED7.cathode, R1.Pin_1

notes:
  12
  11
  10
  9
  8
  7
  Pushbutton on pin 2
  Notification LED on pin 4
  Speaker on pin ~3
