# Fritzing sketch id4236_stoplight_0 (saved by Fritzing 0.7.12b)
breadboards: 1

parts:
  Arduino1 = Arduino
  LED1 = LED - 5mm [color="Red (633nm)" package="5 mm [THT]"]
  LED2 = LED - 5mm [color="Red (633nm)" package="5 mm [THT]"]
  LED3 = LED - 5mm [color="Red (633nm)" package="5 mm [THT]"]

nets:
  N1: Arduino1.GND, LED1.anode, LED2.anode, LED3.anode
  N2: Arduino1.D13, LED1.cathode
  N3: Arduino1.D12, LED2.cathode
  N4: Arduino1.D11, LED3.cathode
