# Fritzing sketch id4237_TrafficLight_0 (saved by Fritzing 0.9.2b)
circuit board: 6.88566cm x 5.36311cm
breadboards: 2

parts:
  LED1 = LED - 5mm [color="Red (633nm)" package="5 mm [THT]"]
  LED2 = LED - 5mm [color="Yellow (592nm)" package="5 mm [THT]"]
  LED3 = LED - 5mm [color="Green (555nm)" package="5 mm [THT]"]
  LED4 = LED - 5mm [color="Red (633nm)" package="5 mm [THT]"]
  LED5 = LED - 5mm [color="Green (555nm)" package="5 mm [THT]"]
  S1 = Pushbutton [package=THT]
  R6 = Resistor [tolerance=±5% resistance=100k package=THT]
  Arduino1 = Arduino Uno (Rev3)
  J1 = Piezo Speaker
  LED6 = smd LED [color="Red (633nm)" package="0603 [SMD]"]
  LED7 = smd LED [color="Yellow (595nm)" package="0603 [SMD]"]
  LED8 = smd LED [color="Green (555nm)" package="0603 [SMD]"]  # not connected

nets (from the breadboard view):
  N1: LED1.cathode, LED2.cathode, LED3.cathode, LED4.cathode, LED5.cathode, R6.Pin_1, Arduino1.GND, LED6.cathode, LED7.cathode
  N2: LED1.anode, Arduino1.D5_PWM
  N3: LED2.anode, Arduino1.D3_PWM
  N4: LED3.anode, Arduino1.D4
  N5: LED4.anode, Arduino1.D9_PWM
  N6: LED5.anode, Arduino1.D8
  N7: S1.leg0, R6.Pin_0, Arduino1.D2
  N8: S1.leg1, Arduino1.5V, J1.pin1, J1.pin2
  N9: Arduino1.D10_PWM/SS, LED6.anode
  N10: Arduino1.D11_PWM/MOSI, LED7.anode

notes:
  Pedestrian Traffic Light
  Car Traffic Light
  This circuit can be coded such that both the car and pedestrian traffic lights go through their normal cycle until the button is pressed by a pedestrian. In this case, the lights will change in favor of the pedestrian.
  bike traffic light
