# Fritzing sketch id4238_Traffic_lights_0 (saved by Fritzing 0.9.3b)
circuit board: 4.83309cm x 2.10577cm
breadboards: 1

parts:
  LED1 = LED - 5mm [color="Green (570nm)" package="5 mm [THT]"]
  LED2 = LED - 5mm [color="Yellow (595nm)" package="5 mm [THT]"]
  LED3 = LED - 5mm [color="Red (633nm)" package="5 mm [THT]"]
  Часть1 = Seeeduino V3.0
  R2 = Resistor [tolerance=±5% resistance=220 package=THT]
  R1 = Resistor [tolerance=±5% resistance=220 package=THT]
  R3 = Resistor [tolerance=±5% resistance=220 package=THT]

nets:
  N1: LED1.cathode, R3.Pin_0
  N2: LED1.anode, Часть1.D6_PWM/A7
  N3: LED2.cathode, R1.Pin_0
  N4: LED2.anode, Часть1.D8/A8
  N5: LED3.cathode, R2.Pin_0
  N6: LED3.anode, Часть1.D10_PWM/A10
  N7: Часть1.GND, R2.Pin_1, R1.Pin_1, R3.Pin_1
