# Fritzing sketch id4241_cam1en2_0 (saved by Fritzing 0.9.3b)
breadboards: 1

parts:
  LED1 = LED - 3mm [color="Red (633nm)" package="3 mm [THT]"]
  LED2 = LED - 3mm [color="Yellow (595nm)" package="3 mm [THT]"]
  LED3 = LED - 3mm [color="Green (570nm)" package="3 mm [THT]"]
  LED4 = LED - 3mm [color="Red (633nm)" package="3 mm [THT]"]
  LED5 = LED - 3mm [color="Yellow (595nm)" package="3 mm [THT]"]
  LED6 = LED - 3mm [color="Green (565nm)" package="3 mm [THT]"]
  R1 = Resistor [tolerance=±5% resistance=220 package="2512 [SMD]"]
  R2 = Resistor [tolerance=±5% resistance=220 package="2512 [SMD]"]
  R3 = Resistor [tolerance=±5% resistance=220 package="2512 [SMD]"]
  R4 = Resistor [tolerance=±5% resistance=220 package="2512 [SMD]"]
  R5 = Resistor [tolerance=±5% resistance=220 package="2512 [SMD]"]
  R6 = Resistor [tolerance=±5% resistance=220 package="2512 [SMD]"]
  S1 = Momentary Switch [package=ksa_sealed_tac_switch]
  S2 = Momentary Switch [package=ksa_sealed_tac_switch]
  Part1 = Arduino Uno (Rev3) - ICSP
  R7 = Resistor [tolerance=±5% resistance=10k package="2512 [SMD]"]
  R8 = Resistor [tolerance=±5% resistance=10k package="2512 [SMD]"]

nets:
  N1: LED1.cathode, LED2.cathode, LED3.cathode, LED4.cathode, LED5.cathode, LED6.cathode, Part1.GND, R7.Pin_0, R8.Pin_0
  N2: LED1.anode, R5.Pin_1
  N3: LED2.anode, R4.Pin_1
  N4: LED3.anode, R6.Pin_1
  N5: LED4.anode, R1.Pin_1
  N6: LED5.anode, R2.Pin_1
  N7: LED6.anode, R3.Pin_1
  N8: R1.Pin_0, Part1.D10_PWM/SS
  N9: R2.Pin_0, Part1.D9_PWM
  N10: R3.Pin_0, Part1.D8
  N11: R4.Pin_0, Part1.ICSP_MISO, Part1.D12/MISO
  N12: R5.Pin_0, Part1.D13/SCK
  N13: R6.Pin_0, Part1.D11_PWM/MOSI
  N14: S1.1, Part1.D2, R8.Pin_1
  N15: S1.4, S2.4, Part1.5V
  N16: S2.1, Part1.D3_PWM, R7.Pin_1
