# Fritzing sketch id4242_SmartVase (saved by Fritzing 0.6.3b)

parts:
  Parte2 = Screen
  Parte3 = Mega
  Parte4 = WiFly
  VCC2 = Battery block 9V  # not connected

nets:
  N1: Parte2.connector0, Parte3.connector27, Parte4.connector17
  N2: Parte2.connector1, Parte3.connector28, Parte4.connector15
  N3: Parte2.connector2, Parte3.connector29, Parte4.connector20
  N4: Parte2.connector3, Parte3.connector18, Parte4.connector19
  N5: Parte2.connector4, Parte3.connector20, Parte4.connector18
  N6: Parte2.connector5, Parte3.connector2, Parte4.connector0
  N7: Parte2.connector6, Parte3.connector0, Parte4.connector1
  N8: Parte2.connector7, Parte3.connector3
  N9: Parte2.connector8, Parte3.connector16
  N10: Parte2.connector9, Parte3.connector17
  N11: Parte3.connector7, Parte4.connector6
  N12: Parte3.connector8, Parte4.connector7
  N13: Parte3.connector9, Parte4.connector14
  N14: Parte3.connector10, Parte4.connector13
  N15: Parte3.connector11, Parte4.connector12
  N16: Parte3.connector12, Parte4.connector11
  N17: Parte3.connector13, Parte4.connector10
  N18: Parte3.connector14, Parte4.connector21
  N19: Parte3.connector21, Parte4.connector2
  N20: Parte3.connector22, Parte4.connector5
  N21: Parte3.connector25, Parte4.connector3
  N22: Parte3.connector26, Parte4.connector4
  N23: Parte3.connector32, Parte4.connector8
  N24: Parte3.connector33, Parte4.connector16
  N25: Parte3.connector34, Parte4.connector9
  N26: Parte3.connector35, Parte4.connector22
  N27: Parte3.connector36, Parte4.connector25
  N28: Parte3.connector37, Parte4.connector24
  N29: Parte3.connector39, Parte4.connector23
  N30: Parte3.connector40, Parte4.connector26
  N31: Parte3.connector41, Parte4.connector27
