# Fritzing sketch id4242_Untitled_Sketch_2_0 (saved by Fritzing 0.9.3b)
breadboards: 1

parts:
  LED1 = LED - 5mm [color="Red (635nm)" package="5 mm [THT]"]
  LED2 = LED - 5mm [color="Green (570nm)" package="5 mm [THT]"]
  LED3 = LED - 5mm [color="Yellow (595nm)" package="5 mm [THT]"]
  Parça1 = Arduino Uno (Rev3)

nets:
  N1: LED1.cathode, LED2.anode, LED3.cathode, Parça1.GND
  N2: LED1.anode, Parça1.D12/MISO
  N3: LED2.cathode, Parça1.D10_PWM/SS
  N4: LED3.anode, Parça1.D11_PWM/MOSI
