# Fritzing sketch id4244_ricetrasmettitore_arduino_0 (saved by Fritzing 0.9.2b)
circuit board: 8.73843cm x 10.5608cm
circuit board: 5.84412cm x 5.83044cm
breadboards: 2

parts:
  Arduino_trasmittente = Arduino Nano (Rev3.0)
  Ricevitore = RF-LINK_RX [package=rf-link_rx]
  Arduino_ricevente = Arduino Nano (Rev3.0)
  Trasmettitore = RF LINK TX 12V
  LED1 = LEDs [package=led10mm]
  R1 = Resistor [tolerance=±5% resistance=330 package="1206 [SMD]"]
  LED2 = LEDs [package=led10mm]
  R2 = Resistor [tolerance=±5% resistance=330 package="1206 [SMD]"]
  LCD1 = LCD screen
  pot_lum = POT [package=pot_alpha_rv16af-20]
  JP1_12V = Header 2 [package=jst-2-pth-kit]
  JP2_12V = Header 2 [package=jst-2-pth-kit]

nets:
  N1: Arduino_trasmittente.GND, Trasmettitore.connector2, R1.Pin_1, JP2_12V.1
  N2: Arduino_trasmittente.D2, Trasmettitore.connector1
  N3: Arduino_trasmittente.VIN, Trasmettitore.connector3, JP2_12V.2
  N4: Arduino_trasmittente.D13/SCK, LED1.A
  GND: Ricevitore.GND, Arduino_ricevente.GND, R2.Pin_1, LCD1.VSS, LCD1.R/W, pot_lum.E, JP1_12V.1
  N5: Ricevitore.DATA, Arduino_ricevente.D6
  +5V: Ricevitore.+5V, Arduino_ricevente.5V, LCD1.VDD, pot_lum.A
  N6: Arduino_ricevente.D2, LCD1.DB7
  N7: Arduino_ricevente.D3, LCD1.DB6
  N8: Arduino_ricevente.D4, LCD1.DB5
  N9: Arduino_ricevente.D5, LCD1.DB4
  N10: Arduino_ricevente.D11/MOSI, LCD1.E
  N11: Arduino_ricevente.D12/MISO, LCD1.RS
  N12: Arduino_ricevente.VIN, JP1_12V.2
  N13: Arduino_ricevente.D13/SCK, LED2.A
  N14: LED1.C, R1.Pin_0
  N15: LED2.C, R2.Pin_0
  N16: LCD1.V0, pot_lum.S
