# Fritzing sketch id4245_tranzistornandgatepushswinledout_rest_0 (saved by Fritzing 0.9.2b)
circuit board: 2.79881cm x 2.22722cm
breadboards: 1

parts:
  Q1 = NPN-Transistor [package="TO92 [THT]"]
  Q2 = NPN-Transistor [package="TO92 [THT]"]
  R3 = Resistor [tolerance=±5% resistance=1k package=THT]
  R2 = Resistor [tolerance=±5% resistance=1k package=THT]
  S1 = Pushbutton [package=THT]
  LED1 = LED - 5mm [color="Red (633nm)" package="5 mm [THT]"]
  S2 = Pushbutton [package=THT]
  R1 = Resistor [tolerance=±5% resistance=1k package=THT]
  VCC1 = 4 x AAA Battery Mount

nets:
  N1: Q1.E, Q2.C
  N2: Q1.B, R2.Pin_1
  N3: Q1.C, LED1.anode, R1.Pin_1
  N4: Q2.E, LED1.cathode, VCC1.-
  N5: Q2.B, R3.Pin_1
  N6: R3.Pin_0, S1.leg0
  N7: R2.Pin_0, S2.leg0
  N8: S1.leg1, S2.leg1, R1.Pin_0, VCC1.+
