# Fritzing sketch id4246_transistor_tester_0 (saved by Fritzing 0.9.2b)
breadboards: 1

parts:
  R1 = Resistor [tolerance=±5% resistance=33k package=THT]
  IC = 555 Timer [package="DIP8 [THT]"]
  VCC1 = Battery block 9V
  C1 = Electrolytic Capacitor [capacitance=10µF voltage=50V package="100 mil [THT, electrolytic]"]
  R2 = Resistor [tolerance=±5% resistance=220 package=THT]
  R3 = Resistor [tolerance=±5% resistance=220 package=THT]
  R4 = Resistor [tolerance=±5% resistance=220 package=THT]
  R5 = Resistor [tolerance=±5% resistance=220 package=THT]
  LED1 = LED - 5mm [color="Red (633nm)" package="5 mm [THT]"]
  LED2 = LED - 5mm [color="Green (565nm)" package="5 mm [THT]"]
  D1 = Rectifier Diode [part_number=1N4148 package="300 mil [THT]"]
  D2 = Rectifier Diode [part_number=1N4148 package="300 mil [THT]"]
  J1 = female pin header, 2 pins [form="♀ (female)"]
  J2 = female pin header, 2 pins [form="♀ (female)"]

nets:
  N1: R1.Pin_0, C1.+
  N2: R1.Pin_1, IC.Trigger, IC.Threshold
  N3: IC.Ground, VCC1.-, C1.-, R4.Pin_1
  N4: IC.Output, R2.Pin_0, LED1.cathode, LED2.anode, J2.pin1
  N5: IC.Reset, IC.Vcc_Supply_Voltage, VCC1.+, R5.Pin_0
  N6: R2.Pin_1, R3.Pin_0, J1.pin2
  N7: R3.Pin_1, R4.Pin_0, R5.Pin_1, LED1.anode, LED2.cathode, D1.cathode, D2.anode
  N8: D1.anode, D2.cathode, J1.pin1

notes:
  C
  B
  E
