# Fritzing sketch id4247_Transistor_Timer_Circuit_0 (saved by Fritzing 0.7.11b)
breadboards: 1

parts:
  VCC1 = Battery block 9V
  R3 = 1k Ω Resistor [package=THT]
  R2 = 22k Ω Resistor [package=THT]
  r1 = 470k Ω Resistor [package=THT]
  LED1 = Red LED - 5mm
  C1 = Electrolytic Capacitor [package=THT]
  S1 = Reed switch [package=THT]
  Q1 = NPN-Transistor [package="TO92 [THT]"]

nets:
  N1: VCC1.-, S1.pin_2, Q1.emitter
  N2: VCC1.+, R3.Pin_0, R2.Pin_0, r1.Pin_0
  N3: R3.Pin_1, LED1.anode
  N4: R2.Pin_1, C1.-, Q1.base
  N5: r1.Pin_1, C1.+, S1.pin_1
  N6: LED1.cathode, Q1.collector
