# Fritzing sketch id4248_Untitled_Sketch_0 (saved by Fritzing 0.9.2b)

parts:
  Part1 = Arduino Mega ADK (Rev3)
  U1 = XBEE-1 [package=xbee-1]  # not connected
  Part2 = XBee Explorer Regulated

nets:
  5V: Part1.IOREF, Part1.5V, Part2.5V
  GND: Part1.GND, Part2.GND
  N1: Part1.D0/RX0, Part2.DOUT
  N2: Part1.D1/TX0, Part2.DIN
