# Fritzing sketch id4250_Tre_led_0 (saved by Fritzing 0.9.3b)
circuit board: 8.46667cm x 5.64444cm
breadboards: 1

parts:
  Componente1 = Arduino Uno (Rev3)
  R1 = Resistor [tolerance=±5% resistance=220 package=THT]
  LED1 = LED - 5mm [color="Red (633nm)" package="5 mm [THT]"]
  LED2 = LED - 5mm [color="Green (565nm)" package="5 mm [THT]"]
  R3 = Resistor [tolerance=±5% resistance=220 package=THT]
  LED3 = LED - 5mm [color="Yellow (592nm)" package="5 mm [THT]"]
  R4 = Resistor [tolerance=±5% resistance=220 package=THT]

nets:
  N1: Componente1.D12/MISO, LED1.anode
  N2: Componente1.GND, R1.Pin_0, R3.Pin_1, R4.Pin_1
  N3: Componente1.D2, LED2.anode
  N4: Componente1.D7, LED3.anode
  N5: R1.Pin_1, LED3.cathode
  N6: LED1.cathode, R3.Pin_0
  N7: LED2.cathode, R4.Pin_0
