# Fritzing sketch id4252_Contiamo_fino_a_3_pot_0 (saved by Fritzing 0.9.1b)
circuit board: 8.46667cm x 5.64444cm
breadboards: 1

parts:
  Componente1 = Arduino Mega ADK (Rev3)
  R1 = Resistor [tolerance=±5% resistance=330 package=THT]
  LED1 = LED - 5mm [color="Red (633nm)" package="5 mm [THT]"]
  R2 = Resistor [tolerance=±5% resistance=330 package=THT]
  LED2 = LED - 5mm [color="Red (633nm)" package="5 mm [THT]"]
  LED3 = LED - 5mm [color="Red (633nm)" package="5 mm [THT]"]
  R3 = Resistor [tolerance=±5% resistance=330 package=THT]
  R4 = Rotary Potentiometer (Small) [maximum_resistance=100kΩ package=THT]

nets:
  N1: Componente1.GND, LED1.cathode, LED2.cathode, LED3.cathode, R4.leg2
  N2: Componente1.D12_PWM, R2.Pin_0
  N3: Componente1.D10_PWM, R1.Pin_0
  N4: Componente1.D8_PWM, R3.Pin_0
  N5: Componente1.5V, R4.leg1
  N6: Componente1.D3_PWM, R4.wiper
  N7: R1.Pin_1, LED2.anode
  N8: LED1.anode, R2.Pin_1
  N9: LED3.anode, R3.Pin_1
