# Fritzing sketch id4254_XBee_Arduino_mini_Trigger_V4_0 (saved by Fritzing 0.9.0b)
circuit board: 3.97341cm x 2.55892cm
breadboards: 1

parts:
  R5 = Resistor [tolerance=±5% resistance=50 package=THT]
  GND = female pin header, 10 pins [form="♀ (female)"]
  OSC = Resonator [package=resonator-smd]
  VCC = female pin header, 2 pins [form="♀ (female)"]
  OPTO = IC, DIP package, 8 pins [chip_label=LTV-826]
  Button = female pin header, 2 pins [form="♀ (female)"]
  Encoder = female pin header, 3 pins [form="♀ (female)"]
  GND/FIN = female pin header, 2 pins [form="♀ (female)"]
  ISP = FTDI_BASIC [package=ftdi_basic]
  MEGA = Arduino Pinout
  C1 = Electrolytic Capacitor [capacitance=10µF package="100 mil [THT, electrolytic]"]
  C2 = Electrolytic Capacitor [capacitance=10µF package="100 mil [THT, electrolytic]"]
  R6 = Resistor [tolerance=±5% resistance=50 package=THT]
  R3 = Resistor [tolerance=±5% resistance=10k package=THT]
  C6 = Ceramic Capacitor [capacitance=0.1µF package="200 mil [THT, multilayer]"]
  C4 = Ceramic Capacitor [capacitance=0.1µF package="200 mil [THT, multilayer]"]
  A2 = female pin header, 4 pins [form="♀ (female)"]
  LDO = Voltage Regulator - Variable [package="TO220 [THT]"]
  A1 = female pin header, 2 pins [form="♀ (female)"]
  F_GND = female pin header, 3 pins [form="♀ (female)"]
  GND/SIN = female pin header, 2 pins [form="♀ (female)"]
  LDO_2 = Voltage Regulator LDO [package=sot23-5]

nets (from the pcb view):
  N1: R5.Pin_0, GND.pin10, ISP.1, ISP.2, MEGA.connector20, R6.Pin_0, C6.1
  N2: R5.Pin_1, OPTO.pin2
  N3: GND.pin2, MEGA.connector15
  N4: GND.pin3, MEGA.connector14
  N5: GND.pin4, MEGA.connector16
  N6: GND.pin5, MEGA.connector11
  N7: GND.pin6, MEGA.connector12
  N8: GND.pin7, MEGA.connector13
  N9: GND.pin8, MEGA.connector1
  N10: GND.pin9, ISP.3, MEGA.connector5, MEGA.connector17, C2.+, R3.Pin_1, LDO.OUT, LDO_2.OUT
  N11: OSC.1, MEGA.connector6
  N12: OSC.2, VCC.pin2, Button.pin2, Encoder.pin2, GND/FIN.pin1, MEGA.connector2, MEGA.connector4, C1.-, C2.-, LDO.ADJ, GND/SIN.pin2, LDO_2.GND
  N13: OSC.3, MEGA.connector7
  N14: VCC.pin1, C1.+, LDO.IN, LDO_2.IN, LDO_2.EN
  N15: OPTO.pin1, MEGA.connector18
  N16: OPTO.pin3, MEGA.connector21
  N17: OPTO.pin4, R6.Pin_1
  N18: OPTO.pin5, OPTO.pin7, F_GND.pin2
  N19: OPTO.pin6, F_GND.pin3
  N20: OPTO.pin8, F_GND.pin1
  N21: Button.pin1, MEGA.connector0
  N22: Encoder.pin1, MEGA.connector31
  N23: Encoder.pin3, MEGA.connector8
  N24: GND/FIN.pin2, MEGA.connector9
  N25: ISP.5, MEGA.connector30
  N26: ISP.6, C4.1
  N27: ISP.4, MEGA.connector29
  N28: MEGA.connector10, GND/SIN.pin1
  N29: MEGA.connector19, C6.0
  N30: MEGA.connector22, A1.pin2
  N31: MEGA.connector23, A1.pin1
  N32: MEGA.connector24, A2.pin1
  N33: MEGA.connector25, A2.pin2
  N34: MEGA.connector26, A2.pin3
  N35: MEGA.connector27, A2.pin4
  N36: MEGA.connector28, R3.Pin_0, C4.0

notes:
  -
  GND
  S
  A
  B
  IN
  GND/FIN
  GND/SIN
  A0
  A5
  A3
  A4
  DTR
  VCC
  SC
  OC
  R
  DC
  SCK
  SO
  CD
  https://github.com/holymoly/triggster
