# Fritzing sketch id4255_trinity_0 (saved by Fritzing 0.9.3b)
circuit board: 11.4359cm x 10.367cm
breadboards: 1

parts:
  ATMEGA_328PU = atmega328 [package=dip]
  S1 = SWITCH-MOMENTARY-2 [package=tactile-pth-12mm]
  S2 = SWITCH-MOMENTARY-2 [package=tactile-pth-12mm]
  S3 = SWITCH-MOMENTARY-2 [package=tactile-pth-12mm]
  S8 = SWITCH-MOMENTARY-2 [package=tactile-pth]
  S9 = SWITCH-MOMENTARY-2 [package=tactile-pth]
  S10 = SWITCH-MOMENTARY-2 [package=tactile-pth]
  S11 = SWITCH-MOMENTARY-2 [package=tactile-pth]
  R1_POTE = Rotary Potentiometer (Small) [maximum_resistance=10kΩ package=THT]
  R2_POTE = Rotary Potentiometer (Small) [maximum_resistance=10kΩ package=THT]
  R3_POTE = Rotary Potentiometer (Small) [maximum_resistance=10kΩ package=THT]
  U2 = Voltage Regulator - 5V [package="TO220 [THT]"]
  AUDIOOUT = AUDIO-JACK2 [package=audio-jack]
  LED1 = LED - 5mm [color="Red (633nm)" package="5 mm [THT]"]
  LED2 = LED - 5mm [color="Red (633nm)" package="5 mm [THT]"]
  LED3 = LED - 5mm [color="Red (633nm)" package="5 mm [THT]"]
  Power_pluG = Power plug
  XTAL1 = Crystal [frequency="16 Mhz" package=THT]
  SWITCH = SWITCH-DPDT [package=eg2211]
  C1 = Electrolytic Capacitor [capacitance=10µF package="100 mil [THT, electrolytic]"]
  R6 = Resistor [tolerance=±5% resistance=1k package=THT]
  R7 = Resistor [tolerance=±5% resistance=1k package=THT]
  R8 = Resistor [tolerance=±5% resistance=1k package=THT]
  R9 = Resistor [tolerance=±5% resistance=220 package=THT]
  D1 = Rectifier Diode [part_number=1N4001 package="300 mil [THT]"]
  C7 = Electrolytic Capacitor [capacitance=10µF package="100 mil [THT, electrolytic]"]
  LED5 = LED - 3mm [color="Red (633nm)" package="3 mm [THT]"]
  LED6 = LED - 3mm [color="Red (633nm)" package="3 mm [THT]"]
  R10 = Resistor [tolerance=±5% resistance=15k package=THT]
  R11 = Resistor [tolerance=±5% resistance=15k package=THT]
  R12 = Resistor [tolerance=±5% resistance=15k package=THT]
  R13 = Resistor [tolerance=±5% resistance=4.9k package=THT]
  R14 = Resistor [tolerance=±5% resistance=38 package=THT]
  R15 = Resistor [tolerance=±5% resistance=220 package=THT]
  C8 = Ceramic Capacitor [capacitance=470nF package="100 mil [THT, multilayer]"]
  C9 = Ceramic Capacitor [capacitance=100nF package="100 mil [THT, multilayer]"]
  R16 = Trimmer Potentiometer [maximum_resistance=10kΩ package=THT]
  C10 = Electrolytic Capacitor [capacitance=1µF package="100 mil [THT, electrolytic]"]
  C11 = Electrolytic Capacitor [capacitance=1µF package="100 mil [THT, electrolytic]"]
  R17 = Resistor [tolerance=±5% resistance=220 package=THT]
  R18 = Resistor [tolerance=±5% resistance=220 package=THT]
  IN = female pin header, 4 pins [form="♀ (female)"]
  OUT = male pin header, 4 pins [form="♂ (male)"]
  clip_bateria = Battery
  C12 = Ceramic Capacitor [capacitance=22pF package="100 mil [THT, multilayer]"]
  C13 = Ceramic Capacitor [capacitance=22pF package="100 mil [THT, multilayer]"]
  LED4 = RGB LED (com. anode, rbg) [package="5 mm [THT]"]

nets:
  N1: ATMEGA_328PU.RESET, R9.Pin_1
  N2: ATMEGA_328PU.D0_(RX), IN.pin1
  N3: ATMEGA_328PU.D1_(TX), OUT.pin1
  N4: ATMEGA_328PU.D2, R8.Pin_0
  N5: ATMEGA_328PU.D3_(PWM), R12.Pin_0
  N6: ATMEGA_328PU.D4, R10.Pin_0
  N7: ATMEGA_328PU.VCC, ATMEGA_328PU.AVCC, ATMEGA_328PU.AREF, R1_POTE.leg2, R2_POTE.leg2, R3_POTE.leg2, U2.output_voltage, LED1.anode, LED2.anode, LED3.anode, R9.Pin_0, C7.+, LED5.cathode, LED6.cathode, IN.pin4, OUT.pin4, LED4.common_anode
  GND: ATMEGA_328PU.GND, S1.2, S2.1, S3.1, S8.2, S9.2, S10.2, S11.2, R1_POTE.leg1, R2_POTE.leg1, R3_POTE.leg1, U2.GND, AUDIOOUT.SLEEVE, C1.-, D1.anode, C7.-, C8.1, C9.1, R16.leg1, IN.pin3, OUT.pin3, C12.0, C13.1
  N8: ATMEGA_328PU.XLAT1, XTAL1.pin_0, C12.1
  N9: ATMEGA_328PU.XLAT2, XTAL1.pin_1, C13.0
  N10: ATMEGA_328PU.D5_(PWM), R11.Pin_0
  N11: ATMEGA_328PU.D6_(PWM), R7.Pin_0
  N12: ATMEGA_328PU.D7, R6.Pin_0
  N13: ATMEGA_328PU.D8, S1.1
  N14: ATMEGA_328PU.D9_(PWM), R14.Pin_1
  N15: ATMEGA_328PU.D10_(PWM), R13.Pin_1
  N16: ATMEGA_328PU.D11_(PWM), S8.1
  N17: ATMEGA_328PU.D12, S3.2
  N18: ATMEGA_328PU.D13, S2.2
  N19: ATMEGA_328PU.A0, S9.1
  N20: ATMEGA_328PU.A1, R3_POTE.wiper
  N21: ATMEGA_328PU.A2, R2_POTE.wiper
  N22: ATMEGA_328PU.A3, S10.1
  N23: ATMEGA_328PU.A4, R1_POTE.wiper
  N24: ATMEGA_328PU.A5, S11.1
  N25: U2.input_voltage, SWITCH.2, SWITCH.1, SWITCH.4, SWITCH.5, C1.+
  N26: AUDIOOUT.RING, AUDIOOUT.RSH, AUDIOOUT.TIP, AUDIOOUT.TSH, R17.Pin_0, R18.Pin_0, OUT.pin2
  N27: LED1.cathode, R8.Pin_1
  N28: LED2.cathode, R7.Pin_1
  N29: LED3.cathode, R6.Pin_1
  N30: Power_pluG.GND, D1.cathode, clip_bateria.-
  N31: Power_pluG.VCC, SWITCH.3, SWITCH.6, clip_bateria.+
  N32: LED5.anode, R12.Pin_1, LED4.red_cathode
  N33: LED6.anode, R11.Pin_1, LED4.green_cathode
  N34: R10.Pin_1, LED4.blue_cathode
  N35: R13.Pin_0, R14.Pin_0, R15.Pin_0, C8.0
  N36: R15.Pin_1, C9.0, R16.leg2
  N37: R16.wiper, C11.+
  N38: C10.-, R18.Pin_1
  N39: C10.+, IN.pin2
  N40: C11.-, R17.Pin_1

notes:
  TRINITY
  DRM.POLY.SQR.MONO
  original project bastl-instruments.com
  FABRICA
  7805
  pines macho
  pines hembra
  jack
  MARCIANA!
