# Fritzing sketch id4256_Trinket_basic_blink_0 (saved by Fritzing 0.9.3b)
breadboards: 1

parts:
  Part1 = trinketpro 5.0
  R1 = Resistor [tolerance=±5% resistance=220 package=THT]
  LED1 = LED - 5mm [color="Red (633nm)" package="5 mm [THT]"]

nets:
  N1: Part1.connector76, R1.Pin_0
  N2: Part1.connector83, LED1.anode
  N3: R1.Pin_1, LED1.cathode

notes:
  Basic Blink Circuit
  + Anode leg of LED to Pin 3
  - Cathode leg of LED to neg rail
  use 220 Ω resistor to neg rail
