# Fritzing sketch id4257_Trinket_LCD_DHT_0 (saved by Fritzing 0.9.3b)
breadboards: 1

parts:
  Part1 = trinketpro 5.0
  DHT1 = DHT11_Temperature_and_Humitidy_Sensor
  U1 = LCD-16X2 [package=lcd-16x2]  # not connected
  Part2 = 16x8 Monochrome LED Backpack

nets:
  N1: Part1.connector76, DHT1.connector4, Part2.connector14
  N2: Part1.connector78, DHT1.connector1, Part2.connector15
  N3: Part1.connector83, DHT1.connector2
  N4: Part1.connector99, Part2.connector13
  N5: Part1.connector100, Part2.connector12

notes:
  LCD Backpack
  SCL (Clock) : Pin A5
  SDA ) : Pin A4
  Ground
  VCC
  DHT11 Humidity Temperature Sensor
  VCC
  Signal (Pin 3)
  n/a
  Ground
