# Fritzing sketch id4258_Trinket_LCD_PhotoCell_LED_0 (saved by Fritzing 0.9.3b)
breadboards: 1

parts:
  Part1 = trinketpro 5.0
  U1 = LCD-16X2 [package=lcd-16x2]  # not connected
  Part2 = 16x8 Monochrome LED Backpack
  R1 = Resistor [tolerance=±5% resistance=10k package=THT]
  R2 = Photocell (LDR) [package=THT]
  LED1 = LED - 5mm [color="Red (633nm)" package="5 mm [THT]"]
  R3 = Resistor [tolerance=±5% resistance=220 package=THT]

nets:
  N1: Part1.connector76, Part2.connector14, R1.Pin_1, R3.Pin_0
  N2: Part1.connector78, Part2.connector15, R2.pin_0
  N3: Part1.connector83, LED1.anode
  N4: Part1.connector96, R1.Pin_0, R2.pin_1
  N5: Part1.connector99, Part2.connector13
  N6: Part1.connector100, Part2.connector12
  N7: LED1.cathode, R3.Pin_1

notes:
  LCD Backpack (4 pins)
  SCL (Clock) : Pin A5
  SDA (Data) : Pin A4
  Ground : GND
  VCC : 5v
  Photocell
  Split voltage circuit
  Pin A1
  10kΩ Resistor
  LED
  Pin 3
  220Ω Resistor
