# Fritzing sketch id4259_Trinket_Piezo_Buzzer_0 (saved by Fritzing 0.9.3b)
breadboards: 1

parts:
  Part1 = trinketpro 5.0
  J1 = Piezo Speaker

nets:
  N1: Part1.connector78, J1.pin1
  N2: Part1.connector83, J1.pin2

notes:
  Pizeo connected to GND
  Pin 3 (PWM)
