# Fritzing sketch id425_practica5_0 (saved by Fritzing 0.9.0b)
breadboards: 1

parts:
  LED2 = smd LED [color="Green (555nm)" package="0805 [SMD]"]
  R1 = Resistor [tolerance=±5% resistance=100 package=THT]
  Parte2 = Bluetooth Mate Silver
  Parte1 = Arduino Uno (Rev3)

nets:
  N1: LED2.cathode, R1.Pin_1
  N2: LED2.anode, Parte1.D4
  N3: R1.Pin_0, Parte2.CTS_5V, Parte1.GND
  N4: Parte2.RX_5V, Parte1.D11_PWM/MOSI
  N5: Parte2.TX_5V, Parte1.D10_PWM/SS
  VCC: Parte2.VCC, Parte1.5V

notes:
  HC-06
  RXD
  TXD
  VCC
  GND
