# Fritzing sketch id4260_Trinket_Pro5v_Pot_RGB_LED_0 (saved by Fritzing 0.9.3b)
breadboards: 1

parts:
  Part1 = trinketpro 5.0
  R1 = Rotary Potentiometer (Small) [maximum_resistance=100kΩ package=THT]
  R5 = Resistor [tolerance=±5% resistance=220 package=THT]
  LED1 = RGB LED (com. cathode, rgb) [package="5 mm [THT]"]
  R6 = Resistor [tolerance=±5% resistance=220 package=THT]
  R7 = Resistor [tolerance=±5% resistance=220 package=THT]

nets:
  N1: Part1.connector76, R1.leg2, LED1.common_cathode
  N2: Part1.connector78, R1.leg1
  N3: Part1.connector81, R5.Pin_0, R5.Pin_1, LED1.red_anode
  N4: Part1.connector82, LED1.green_anode, R6.Pin_0, R6.Pin_1
  N5: Part1.connector83, LED1.blue_anode, R7.Pin_0, R7.Pin_1
  N6: Part1.connector95, R1.wiper

notes:
  Potentiometer Pin A0
  RGB LED Pins 5, 4, 3
  Common cathode, long pin negative
