# Fritzing sketch id4261_Trinket_Pro_Servo_0 (saved by Fritzing 0.9.3b)
breadboards: 1

parts:
  Part1 = trinketpro 5.0
  J1 = Basic Servo

nets:
  N1: Part1.connector76, J1.gnd
  N2: Part1.connector78, J1.vcc
  N3: Part1.connector89, J1.pulse

notes:
  Servo wires:
  Brown- Ground
  Orange: 5V
  Yellow: Signal - Pin 9
