# Fritzing sketch id4263_Trinket_Theremin_0 (saved by Fritzing 0.9.1b)
breadboards: 1

parts:
  Part1 = trinketpro 5.0
  J1 = Piezo Speaker
  R1 = PHOTOCELL [package=photocell]
  R2 = Resistor [tolerance=±5% resistance=220 package="1206 [SMD]"]

nets:
  N1: Part1.connector76, J1.pin1, R2.Pin_0
  N2: Part1.connector78, Part1.connector96, R1.P$1, R1.P$2, R2.Pin_1
  N3: Part1.connector86, J1.pin2
