# Fritzing sketch id4265_Triv2_0 (saved by Fritzing 0.9.1b)
breadboards: 2

parts:
  Teensy_3_1 = Teensy 3.1
  S1 = Pushbutton [package="[THT]"]
  S2 = Pushbutton [package="[THT]"]
  S3 = Pushbutton [package="[THT]"]
  S4 = Pushbutton [package="[THT]"]
  S5 = Pushbutton [package="[THT]"]
  S6 = Pushbutton [package="[THT]"]
  S7 = Pushbutton [package="[THT]"]
  S8 = Pushbutton [package="[THT]"]
  S9 = Pushbutton [package="[THT]"]
  S10 = Pushbutton [package="[THT]"]
  S11 = Pushbutton [package="[THT]"]
  VCC1 = 4 x AAA Battery Mount
  Part1 = Audio Jack Breakout
  Q1 = NPN-Transistor [package="TO92 [THT]"]
  R1 = Resistor [tolerance=±5% resistance=100 package=THT]
  R2 = Resistor [tolerance=±5% resistance=4.7k package=THT]
  C2 = Electrolytic Capacitor [capacitance=10µF package="0405 [SMD, electrolytic]"]
  C1 = Electrolytic Capacitor [capacitance=10µF package="100 mil [THT, electrolytic]"]

nets:
  GND: Teensy_3_1.GND, S1.Pin_3, S1.Pin_4, S2.Pin_3, S2.Pin_4, S3.Pin_3, S3.Pin_4, S4.Pin_3, S4.Pin_4, S5.Pin_3, S5.Pin_4, S6.Pin_3, S6.Pin_4, S7.Pin_3, S7.Pin_4, S8.Pin_3, S8.Pin_4, S9.Pin_3, S9.Pin_4, S10.Pin_3, S10.Pin_4, S11.Pin_3, S11.Pin_4, VCC1.-, Part1.GND, R1.Pin_0
  N1: Teensy_3_1.D0, S1.Pin_1, S1.Pin_2
  N2: Teensy_3_1.D1, S2.Pin_1, S2.Pin_2
  N3: Teensy_3_1.D2, S3.Pin_1, S3.Pin_2
  N4: Teensy_3_1.D3, S4.Pin_1, S4.Pin_2
  N5: Teensy_3_1.D4, S5.Pin_1, S5.Pin_2
  N6: Teensy_3_1.D5, S6.Pin_1, S6.Pin_2
  N7: Teensy_3_1.D6, S7.Pin_1, S7.Pin_2
  N8: Teensy_3_1.D7, S8.Pin_1, S8.Pin_2
  N9: Teensy_3_1.D8, S9.Pin_1, S9.Pin_2
  N10: Teensy_3_1.D9, S10.Pin_1, S10.Pin_2
  N11: Teensy_3_1.D10, S11.Pin_1, S11.Pin_2
  N12: Teensy_3_1.A14/DAC, C2.-
  N13: Teensy_3_1.Vin, VCC1.+, Q1.C, R2.Pin_1
  N14: Part1.RING, Part1.TIP, C1.-
  N15: Q1.E, R1.Pin_1, C1.+
  N16: Q1.B, R2.Pin_0, C2.+

notes:
  The Teensy doesn't want to get more than 6 volts, so it's not a bad idea to remove one of the batteries and solder a shorting wire in its place.
  Program the Teensy, plug earbuds into the 3.5 mm jack, and start hitting pushbuttons.
