# Fritzing sketch id4267_VerdadeOuMentira_0 (saved by Fritzing 0.7.12b)
breadboards: 1

parts:
  LED1 = LED - 5mm [color="Red (633nm)" package="5 mm [THT]"]
  LED2 = smd LED [color="Green (555nm)" package="0603 [SMD]"]
  S1 = Pushbutton [package="[THT]"]
  R1 = Resistor [tolerance=±5% resistance=470 package=THT]
  R2 = Resistor [tolerance=±5% resistance=47k package=THT]
  3V = Battery
  MSP430G2221 = IC, DIP package, 14 pins [chip_label=MSP430G221]

nets:
  N1: LED1.cathode, LED2.cathode, R1.Pin_1
  N2: LED1.anode, MSP430G2221.pin2
  N3: LED2.anode, MSP430G2221.pin8
  N4: S1.Pin_1, S1.Pin_2, R2.Pin_1, MSP430G2221.pin5
  N5: S1.Pin_3, S1.Pin_4, 3V.+, MSP430G2221.pin1
  N6: R1.Pin_0, R2.Pin_0, 3V.-, MSP430G2221.pin14
