# Fritzing sketch id4268_TrueRNG_1.2_0 (saved by Fritzing 0.7.12b)
breadboards: 1

parts:
  Q1 = NPN-Transistor [package="TO92 [THT]"]
  Q2 = NPN-Transistor [package="TO92 [THT]"]
  Q3 = NPN-Transistor [package="TO92 [THT]"]
  4K7 = Resistor [tolerance=±5% resistance=4.7k package=THT]
  4K7_2 = Resistor [tolerance=±5% resistance=4.7k package=THT]
  1M = Resistor [tolerance=±5% resistance=1M package=THT]
  4K7_3 = Resistor [tolerance=±5% resistance=4.7k package=THT]
  Arduino1 = Arduino
  5V-12V = mystery part, 3 pins [chip_label=?]
  C1 = Ceramic Capacitor [capacitance=100nF package="200 mil [THT, multilayer]"]

nets:
  N1: Q1.E, Q2.C, 4K7.Pin_1, C1.0
  N2: Q1.B, Q2.B
  GND: Q2.E, Q3.E, 4K7_3.Pin_1, Arduino1.GND, 5V-12V.pin2
  N3: Q3.B, 1M.Pin_1, C1.1
  N4: Q3.C, 4K7_2.Pin_1, 4K7_3.Pin_0, Arduino1.A0
  N5: 4K7.Pin_0, 5V-12V.pin3
  5V: 4K7_2.Pin_0, 1M.Pin_0, Arduino1.+5V, 5V-12V.pin1

notes:
  TrueRNG 1.2
