# Fritzing sketch id4269_test_0 (saved by Fritzing 0.9.3b)
breadboards: 1

parts:
  Part2 = RFID-RC522
  Part1 = Arduino Uno (Rev3) - ICSP
  VCC1 = Battery  # not connected
  M1 = DC Motor  # not connected
  U1 = TOUCH [package=touch2]  # not connected
  U2 = TOUCH [package=touch2]  # not connected
  Composant1 = Arduino Motor Shield

nets:
  N1: Part2.connector8, Part1.D10_PWM/SS
  N2: Part2.connector9, Part1.D13/SCK
  N3: Part2.connector10, Part1.D11_PWM/MOSI
  N4: Part2.connector11, Part1.D12/MISO
  N5: Part2.connector13, Part1.GND
  N6: Part2.connector14, Part1.D9_PWM
  N7: Part2.connector15, Part1.3V3
  VIN: Part1.VIN, Composant1.VIN
