# Fritzing sketch id426_Arduino_bluetooth_rc_car_4w_applicazione_0 (saved by Fritzing 0.9.2b)
breadboards: 2

parts:
  Part1 = Arduino Uno (Rev3)
  Part2 = bluetooth-module
  S1 = Ponte-H L298N
  M1 = DC Motor
  M2 = DC Motor
  VCC1 = Battery block 9V
  M3 = DC Motor
  M4 = DC Motor
  VCC2 = 4 x AAA Battery Mount  # not connected
  VCC3 = 4 x AAA Battery Mount  # not connected
  U1 = SWITCH-SPST-2 [package=switch-spst-vertical]  # not connected
  LED1 = smd LED [color="Red (633nm)" package="0603 [SMD]"]
  LED2 = smd LED [color="Red (633nm)" package="1206 [SMD]"]
  LED3 = smd LED [color="Orange (605nm)" package="1206 [SMD]"]
  LED4 = smd LED [color="Orange (605nm)" package="1206 [SMD]"]
  R1 = Resistor [tolerance=±5% resistance=220 package=THT]
  J1 = Piezo Speaker
  R2 = Resistor [tolerance=±5% resistance=220 package=THT]
  LED5 = LED - 5mm [color="Orange (605nm)" package="5 mm [THT]"]
  LED6 = LED - 5mm [color="Orange (605nm)" package="5 mm [THT]"]
  LED7 = LED - 5mm [color="White (6500K)" package="5 mm [THT]"]
  LED8 = LED - 5mm [color="White (6500K)" package="5 mm [THT]"]
  R3 = Resistor [tolerance=±5% resistance=220 package=THT]
  R4 = Resistor [tolerance=±5% resistance=220 package=THT]

nets:
  N1: Part1.D9_PWM, R2.Pin_0
  N2: Part1.D10_PWM/SS, S1.connector7
  N3: Part1.D11_PWM/MOSI, S1.connector8
  N4: Part1.D12/MISO, R1.Pin_0
  N5: Part1.D13/SCK, R4.Pin_1
  N6: Part1.D0/RX, Part2.connector15
  N7: Part1.D1/TX, Part2.connector16
  N8: Part1.D3_PWM, J1.pin2
  N9: Part1.D5_PWM, S1.connector5
  N10: Part1.D6_PWM, S1.connector6
  N11: Part1.5V, Part2.connector13
  N12: Part1.GND, Part2.connector14, S1.connector2, VCC1.-
  N13: Part1.VIN, VCC1.+
  N14: S1.connector4, S1.connector15
  N15: S1.connector9, S1.connector16
  N16: S1.connector10, M1.pin_2
  N17: S1.connector11, M1.pin_1, M4.pin_1
  N18: S1.connector13, M2.pin_2, M3.pin_2
  N19: S1.connector14, M2.pin_1, M3.pin_1
  N20: LED1.cathode, LED2.anode
  N21: LED1.anode, R1.Pin_1
  N22: LED2.cathode, LED4.cathode, J1.pin1
  N23: LED3.cathode, LED4.anode
  N24: LED3.anode, R2.Pin_1
  N25: LED5.cathode, LED7.cathode
  N26: LED5.anode, LED6.cathode
  N27: LED6.anode, R3.Pin_0
  N28: LED7.anode, LED8.cathode
  N29: LED8.anode, R4.Pin_0

notes:
  Arduino Bluetooth RC Car
  www.progettiarduino.com
