# Fritzing sketch id4270_TrafficLightController_0 (saved by Fritzing 0.8.7b)
breadboards: 1

parts:
  Arduino = Arduino Uno (Rev3)
  LED1 = LED - 5mm [color="Red (633nm)" package="5 mm [THT]"]
  LED2 = LED - 5mm [color="Green (555nm)" package="5 mm [THT]"]
  LED3 = LED - 5mm [color="Red (633nm)" package="5 mm [THT]"]
  LED4 = LED - 5mm [color="Green (555nm)" package="5 mm [THT]"]
  LED5 = LED - 5mm [color="Red (633nm)" package="5 mm [THT]"]
  R1 = Resistor [tolerance=±5% resistance=470 package=THT]
  LED6 = LED - 5mm [color="Red (633nm)" package="5 mm [THT]"]
  LED7 = LED - 5mm [color="Green (555nm)" package="5 mm [THT]"]
  LED8 = LED - 5mm [color="Green (555nm)" package="5 mm [THT]"]
  R2 = Resistor [tolerance=±5% resistance=470 package=THT]
  R3 = Resistor [tolerance=±5% resistance=470 package=THT]
  R4 = Resistor [tolerance=±5% resistance=470 package=THT]
  R5 = Resistor [tolerance=±5% resistance=470 package=THT]
  R6 = Resistor [tolerance=±5% resistance=470 package=THT]
  R7 = Resistor [tolerance=±5% resistance=470 package=THT]
  R8 = Resistor [tolerance=±5% resistance=470 package=THT]
  U1 = 74HC595 [part_number=74HC595N package="DIP16 [THT]"]

nets:
  N1: Arduino.D3_PWM, U1.DS
  N2: Arduino.D4, U1.ST_CP
  N3: Arduino.D5_PWM, U1.SH_CP
  5V: Arduino.5V, U1.MR, U1.VCC
  GND: Arduino.GND, R1.Pin_1, R2.Pin_1, R3.Pin_1, R4.Pin_1, R5.Pin_1, R6.Pin_1, R7.Pin_1, R8.Pin_1, U1.GND, U1.OE
  N4: LED1.cathode, R1.Pin_0
  N5: LED1.anode, U1.Q0
  N6: LED2.cathode, R2.Pin_0
  N7: LED2.anode, U1.Q1
  N8: LED3.cathode, R3.Pin_0
  N9: LED3.anode, U1.Q2
  N10: LED4.cathode, R4.Pin_0
  N11: LED4.anode, U1.Q3
  N12: LED5.cathode, R7.Pin_0
  N13: LED5.anode, U1.Q6
  N14: LED6.cathode, R5.Pin_0
  N15: LED6.anode, U1.Q4
  N16: LED7.cathode, R6.Pin_0
  N17: LED7.anode, U1.Q5
  N18: LED8.anode, U1.Q7

notes:
  8 Led's are controlled in 4 groups.
  IC is controlled by sending a number to it which is converted to binary via the IC and then used to either turn on or turn off an LED.
  Grp 1
  Grp 2
  Grp 3
  Grp 4
