# Fritzing sketch id4271_robotika_0 (saved by Fritzing 0.8.5b)
breadboards: 2

parts:
  Part1 = Arduino Uno (Rev3)
  M1 = DC Motor
  M2 = DC Motor
  IC1 = L293D [package=THT]
  VCC1 = 4 x AAA Battery Mount
  Part2 = SRF05 Ultrasonic Rangefinder

nets:
  N1: Part1.D8, Part2.connector10
  N2: Part1.D9_PWM, Part2.connector9
  N3: Part1.D12/MISO, IC1.In_3
  N4: Part1.GND, IC1.0V, VCC1.-, Part2.connector11
  N5: Part1.D2, IC1.In_4
  N6: Part1.D4, IC1.In_1
  N7: Part1.D5_PWM, IC1.In_2
  N8: Part1.5V, IC1.Enable_2, IC1.+V
  N9: M1.pin_1, IC1.Out_2_(_Controlled_by_Enable_1_)
  N10: M1.pin_2, IC1.Out_1_(_Controlled_by_Enable_1_)
  N11: M2.pin_1, IC1.Out_4_(_Controlled_by_Enable_2_)
  N12: M2.pin_2, IC1.Out_3_(_Controlled_by_Enable_2_)
  N13: IC1.Enable_1, Part2.connector8
  N14: IC1.+Vmotor, VCC1.+
