# Fritzing sketch id4272_ATMega1284P_Turbuino_0 (saved by Fritzing 0.8.7b)
circuit board: 11.5cm x 10cm
breadboards: 1

parts:
  XTAL1 = Crystal [frequency="16 Mhz" package=THT]
  Atmega1 = ATMEGA1284P
  C1 = Ceramic Capacitor [capacitance=22pF voltage=5V package="100 mil [THT, multilayer]"]
  C2 = Ceramic Capacitor [capacitance=22pF voltage=5V package="100 mil [THT, multilayer]"]
  S1 = Pushbutton [package="[THT]"]
  R1 = Resistor [tolerance=±5% resistance=10k package=THT]
  U1 = PA07Header
  U2 = PrimaryHeader1284P
  J1 = JTAG1284P
  U4 = PBD442Header
  J2 = Power1284P

nets:
  N1: XTAL1.pin_0, Atmega1.connector12, C1.1
  N2: XTAL1.pin_1, Atmega1.connector11, C2.0
  N3: Atmega1.connector0, U4.connector0
  N4: Atmega1.connector1, U4.connector1
  N5: Atmega1.connector2, U4.connector2
  N6: Atmega1.connector3, U4.connector3
  N7: Atmega1.connector5, U2.connector5
  N8: Atmega1.connector6, U2.connector4
  N9: Atmega1.connector7, U2.connector3
  N10: Atmega1.connector8, S1.Pin_1, S1.Pin_2, R1.Pin_1, U2.connector2
  N11: Atmega1.connector9, Atmega1.connector29, R1.Pin_0, U2.connector0, J1.connector4, J2.connector0, J2.connector4
  N12: Atmega1.connector10, Atmega1.connector30, C1.0, C2.1, S1.Pin_3, S1.Pin_4, U2.connector1, J1.connector5
  N13: Atmega1.connector13, U2.connector7
  N14: Atmega1.connector14, U2.connector6
  N15: Atmega1.connector15, U4.connector4
  N16: Atmega1.connector16, U4.connector5
  N17: Atmega1.connector17, U4.connector6
  N18: Atmega1.connector18, U4.connector7
  N19: Atmega1.connector19, U4.connector8
  N20: Atmega1.connector20, U4.connector9
  N21: Atmega1.connector21, U1.connector9
  N22: Atmega1.connector22, U1.connector8
  N23: Atmega1.connector23, J1.connector3
  N24: Atmega1.connector24, J1.connector2
  N25: Atmega1.connector25, J1.connector1
  N26: Atmega1.connector26, J1.connector0
  N27: Atmega1.connector32, U1.connector7
  N28: Atmega1.connector33, U1.connector6
  N29: Atmega1.connector34, U1.connector5
  N30: Atmega1.connector35, U1.connector4
  N31: Atmega1.connector36, U1.connector3
  N32: Atmega1.connector37, U1.connector2
  N33: Atmega1.connector38, U1.connector1
  N34: Atmega1.connector39, U1.connector0
  N35: U2.connector8, J2.connector2
  N36: U2.connector9, J2.connector1, J2.connector3, J2.connector5
