# Fritzing sketch id4273_TurbuinoShield_0 (saved by Fritzing 0.8.7b)
circuit board: 6.88566cm x 5.36311cm

parts:
  Part1 = Arduino Uno (Rev3)
  U1 = PrimaryHeader1284P

nets:
  N1: Part1.D10_PWM/SS, U1.connector2
  N2: Part1.D11_PWM/MOSI, U1.connector5
  N3: Part1.D12/MISO, U1.connector4
  N4: Part1.D13/SCK, U1.connector3
  N5: Part1.D0/RX, U1.connector7
  N6: Part1.D1/TX, U1.connector6
  N7: Part1.5V, U1.connector0
  N8: Part1.GND, U1.connector1
