# Fritzing sketch id4275_Turn_Signals_&_Flashers_Simulation_0 (saved by Fritzing 0.9.3b)
circuit board: 8.46667cm x 5.64444cm
breadboards: 1

parts:
  S3 = Taiway 100-SP-X-T1 SPDT Miniature Toggle Switch [part_number="SPDT Center Off (Flasher Mode)" package=THT]
  S4 = Taiway 100-SP-X-T1 SPDT Miniature Toggle Switch [part_number="SPDT Center Off (Turn Siganl)" package=THT]
  S2 = Taiway 100-SP-X-T1 SPDT Miniature Toggle Switch [part_number="SPDT (Flashers)" package=THT]
  S1 = Taiway 100-SP-X-T1 SPDT Miniature Toggle Switch [part_number="SPDT Momentary (Brake)" package=THT]
  R1 = Resistor [tolerance=±5% resistance=10k package="2010 [SMD]"]
  R2 = Resistor [tolerance=±5% resistance=10k package="2010 [SMD]"]
  R3 = Resistor [tolerance=±5% resistance=10k package="2010 [SMD]"]
  R4 = Resistor [tolerance=±5% resistance=10k package="2010 [SMD]"]
  R5 = Resistor [tolerance=±5% resistance=10k package="2010 [SMD]"]
  R6 = Resistor [tolerance=±5% resistance=10k package="2010 [SMD]"]
  R7 = Resistor [tolerance=±5% resistance=470 package="2010 [SMD]"]
  Part2 = ws2812b [package="smd 2812b"]
  Part3 = ws2812b [package="smd 2812b"]
  Part5 = ws2812b [package="smd 2812b"]
  Part6 = ws2812b [package="smd 2812b"]
  Part7 = ws2812b [package="smd 2812b"]
  Part8 = ws2812b [package="smd 2812b"]
  Part9 = ws2812b [package="smd 2812b"]
  Part4 = ws2812b [package="smd 2812b"]
  Part1 = Arduino Nano (Rev3.0)

nets:
  VDD: S3.COM, S4.COM, S2.COM, S1.COM, Part2.VDD, Part3.VDD, Part5.VDD, Part6.VDD, Part7.VDD, Part8.VDD, Part9.VDD, Part4.VDD, Part1.5V
  N1: S3.L1, R5.Pin_1, Part1.D12/MISO
  N2: S3.L2, R6.Pin_0, Part1.D13/SCK
  N3: S4.L1, R3.Pin_1, Part1.D9
  N4: S4.L2, R2.Pin_1, Part1.D8
  N5: S2.L1, R1.Pin_1, Part1.D11/MOSI
  N6: S1.L1, R4.Pin_1, Part1.D10
  VSS: R1.Pin_0, R2.Pin_0, R3.Pin_0, R4.Pin_0, R5.Pin_0, R6.Pin_1, Part2.VSS, Part3.VSS, Part5.VSS, Part6.VSS, Part7.VSS, Part8.VSS, Part9.VSS, Part4.VSS, Part1.GND
  N7: R7.Pin_0, Part1.D6
  N8: R7.Pin_1, Part2.DIN
  N9: Part2.DOUT, Part3.DIN
  N10: Part3.DOUT, Part4.DIN
  N11: Part5.DOUT, Part6.DIN
  N12: Part5.DIN, Part4.DOUT
  N13: Part6.DOUT, Part7.DIN
  N14: Part7.DOUT, Part8.DIN
  N15: Part8.DOUT, Part9.DIN

notes:
  S3 Modes:
  UP - Security Flashers
  Middle - Emergency Flashers
  DOWN - Police Flashers
  S4 Modes:
  LeftTurn - OFF - Right Turn
