# Fritzing sketch id4276_turn_signal_0 (saved by Fritzing 0.7.11b)
breadboards: 1

parts:
  U1 = atmega168 [package=dip]
  LED1 = LED - 5mm [color="Red (633nm)" package="5 mm [THT]"]
  LED2 = LED - 5mm [color="Red (633nm)" package="5 mm [THT]"]

nets:
  N1: U1.D2, U1.D3_(PWM)
  N2: U1.D12, U1.D13, LED1.cathode, LED2.cathode
  N3: U1.GND#21, LED1.anode, LED2.anode
