# Fritzing sketch id427_Arduino_bluetooth_serial_example_0 (saved by Fritzing 0.9.0b)
breadboards: 1

parts:
  부품1 = Arduino Uno (Rev3)
  부품2 = HC-06

nets:
  N1: 부품1.D10_PWM/SS, 부품2.connector13
  N2: 부품1.D11_PWM/MOSI, 부품2.connector12
  N3: 부품1.5V, 부품2.connector15
  N4: 부품1.GND, 부품2.connector14
