# Fritzing sketch id4280_TurretControlCircuitMay18_code_0 (saved by Fritzing 0.9.3b)
breadboards: 2

parts:
  Part1 = Arduino Mega 2560 (Rev3)
  LED1 = LED - 5mm [color="Red (633nm)" package="5 mm [THT]"]
  R1 = Rotary Potentiometer (Small) [maximum_resistance=100kΩ package=THT]
  U1 = prefix0000
  M1 = Stepper Motor - Bipolar
  S1 = Momentary Switch [package=ksa_sealed_tac_switch]
  S2 = Momentary Switch [package=ksa_sealed_tac_switch]
  R2 = TRIMPOT [package=trimpot_pth_s3_lock]
  LCD1 = LCD screen
  R3 = prefix0000
  R4 = prefix0000
  C1 = Ceramic Capacitor [capacitance=100nF package="100 mil [THT, multilayer]"]
  C2 = Ceramic Capacitor [capacitance=100nF package="100 mil [THT, multilayer]"]
  IC1 = prefix0000
  C3 = Ceramic Capacitor [capacitance=100nF package="100 mil [THT, multilayer]"]
  R5 = prefix0000
  D1 = Rectifier Diode [part_number=1N4001 package="300 mil [THT]"]
  C5 = prefix0000
  R6 = TRIMPOT [package=trimpot_pth_s3_lock]

nets:
  N1: Part1.A0, R1.wiper
  N2: Part1.D21/SCL, LCD1.RS
  N3: Part1.D19/RX1, LCD1.DB4
  N4: Part1.D18/TX1, LCD1.DB5
  N5: Part1.D17_PWM/RX2, LCD1.DB6
  N6: Part1.D16_PWM/TX2, LCD1.DB7
  N7: Part1.D13_PWM, LED1.anode
  N8: Part1.D12_PWM, U1.connector0
  N9: Part1.D11_PWM, U1.connector1
  N10: Part1.D10_PWM, U1.connector2
  N11: Part1.D9_PWM, U1.connector3
  5V: Part1.5V, R1.leg1, R2.CCW, LCD1.VDD, LCD1.LED+
  GND: Part1.GND, LED1.cathode, R1.leg2, R2.CW, LCD1.VSS, LCD1.R/W, LCD1.LED-, R3.connector1, R4.connector0, C1.1, C2.1
  N12: Part1.D2_PWM, S1.3, S1.4, C1.0
  N13: Part1.D3_PWM, S2.3, S2.4, C2.0
  N14: U1.connector7, C3.1, C5.connector0, R6.CW
  N15: U1.connector8, C3.0, R5.connector1, D1.cathode
  N16: U1.connector12, M1.A
  N17: U1.connector13, M1.C
  N18: U1.connector14, M1.B
  N19: U1.connector15, M1.D
  N20: S1.1, S1.2, R3.connector0
  N21: S2.1, S2.2, R4.connector1
  N22: R2.WIPER, LCD1.V0
  N23: IC1.connector0, R5.connector0, D1.anode, C5.connector1, R6.CCW, R6.WIPER

notes:
  *The stepper motor that is shown is NOT the motor that is on my protoboard
  StepperMTR is: 28BYJ-48
  Driver is: SBT0811/ULN2003APG
  Vol Reg LM350T with adjustable pin#1(GND)
