# Fritzing sketch id4281_TurretControlCircuitMAY22_0 (saved by Fritzing 0.9.3b)
breadboards: 3

parts:
  LED1 = LED - 5mm [color="Red (633nm)" package="5 mm [THT]"]
  U1 = prefix0000
  S1 = Momentary Switch [package=ksa_sealed_tac_switch]
  S2 = Momentary Switch [package=ksa_sealed_tac_switch]
  LCD1 = LCD screen
  R3 = prefix0000
  R4 = prefix0000
  IC1 = prefix0000
  R5 = prefix0000
  U4 = prefix0000
  JP2 = Header 5x2 [package=2x5-shrouded_smd]
  JP3 = Header 5x2 [package=2x5-shrouded_smd]
  JP4 = M16 [package=1x16_machine-pin-header_lock.004]
  U5 = LIPO-110mAh [package=lipo-110]
  D1 = prefix0000 [part_number=1N4004]
  R6 = prefix0000
  R7 = prefix0000
  R8 = prefix0000
  C4 = prefix0000
  C5 = prefix0000
  C6 = prefix0000
  C7 = prefix0000

nets:
  N1: LED1.cathode, LCD1.VSS, LCD1.R/W, LCD1.LED-, R3.connector1, U5.-, R8.connector2, C6.connector1
  N2: LED1.anode, JP4.16
  N3: U1.connector0, U1.connector1, U1.connector2, U1.connector3, U1.connector4, U1.connector5, U1.connector10, U1.connector11, U1.connector12, U1.connector13, U1.connector14, U1.connector15, JP2.1, JP2.2, JP2.3, JP2.4, JP2.5, JP2.6, JP2.7, JP2.8, JP2.9, JP2.10, JP3.1, JP3.2, JP3.3, JP3.4, JP3.5, JP3.6, JP3.7, JP3.8, JP3.9, JP3.10
  N4: U1.connector6, U1.connector9
  N5: U1.connector7, U1.connector8, IC1.connector1, IC1.connector2, R5.connector1, U4.connector0, U4.connector1, D1.connector0, R6.connector2, C4.connector0, C5.connector0, C5.connector1
  N6: S1.1, S1.2, R3.connector0
  N7: S1.3, S1.4, JP4.3, C7.connector0
  N8: S2.1, S2.2, R4.connector1
  N9: S2.3, S2.4, JP4.2, C6.connector0
  N10: LCD1.VDD, LCD1.LED+, U5.+, R7.connector0, R7.connector2, R8.connector0
  N11: LCD1.V0, R7.connector1
  N12: LCD1.RS, JP4.5
  N13: LCD1.E, JP4.6
  N14: LCD1.DB4, JP4.12
  N15: LCD1.DB5, JP4.13
  N16: LCD1.DB6, JP4.14
  N17: LCD1.DB7, JP4.15
  N18: R4.connector0, C7.connector1
  N19: IC1.connector0, R5.connector0, D1.connector1, R6.connector0, R6.connector1, C4.connector1
  N20: JP4.1, R8.connector1

notes:
  Driver is: SBT0811/ULN2003APG
  12vdc 1A
  5vdc 110mAh
