# Fritzing sketch id4283_Starting_Electronics___Tutorial_1_0 (saved by Fritzing 0.7.11b)
breadboards: 1

parts:
  VCC1 = Battery block 9V
  R1 = 1k Ω Resistor [package=THT]
  LED1 = LED - 5mm [color="Red (633nm)" package="5 mm [THT]"]

nets:
  N1: VCC1.-, R1.Pin_0
  N2: VCC1.+, LED1.anode
  N3: R1.Pin_1, LED1.cathode
