# Fritzing sketch id4289_Current_Source_0 (saved by Fritzing 0.8.5b)
breadboards: 1

parts:
  U1 = LM358 [package=dip08]
  R1 = Resistor [tolerance=±5% resistance=220 package=THT]
  R2 = Trimmer Potentiometer [maximum_resistance=10kΩ package=THT]  # not connected

nets:
  N1: U1.G$1_OUT, R1.Pin_0
  N2: U1.G$1_-IN, R1.Pin_1
  N3: U1.G$1_+IN, U1.G$1_V-
