# Fritzing sketch id428_Arduino_Bootloader_e_Uploader_0 (saved by Fritzing 0.8.7b)
breadboards: 1

parts:
  Componente1 = Arduino Uno (Rev3)
  U1 = atmega328 [package=dip]
  R1 = Resistor [tolerance=±5% resistance=10k package=THT]
  C1 = Capacitor [package=cap-pth-small2]
  C2 = Capacitor [part_number="22 uF" package=cap-pth-small2]
  XTAL1 = Crystal [frequency="16 Mhz" package=SMD]
  R6 = Resistor [tolerance=±5% resistance=220 package=THT]
  LED3 = LED - 3mm [color="Green (555nm)" package="3 mm [THT]"]
  C10 = Capacitor [part_number="22 uf" package=cap-pth-small2]
  S3 = Pushbutton [package="[THT]"]
  LED4 = LED - 3mm [color="Red (633nm)" package="3 mm [THT]"]  # not connected
  R7 = Resistor [tolerance=±5% resistance=220 package=THT]

nets:
  N1: Componente1.D10_PWM/SS, U1.RESET, R1.Pin_0, C10.2, S3.Pin_3, S3.Pin_4
  N2: Componente1.D11_PWM/MOSI, U1.D11_(PWM)
  N3: Componente1.D12/MISO, U1.D12
  N4: Componente1.D13/SCK, U1.D13, LED3.anode
  N5: Componente1.5V, R1.Pin_1
  N6: Componente1.GND, C1.1, C2.2, R6.Pin_1, C10.1, S3.Pin_1, S3.Pin_2, R7.Pin_1
  N7: U1.XLAT1, C2.1, XTAL1.pin_1
  N8: U1.XLAT2, C1.2, XTAL1.pin_0
  N9: R6.Pin_0, LED3.cathode
