# Fritzing sketch id4290_tvgone_1.2_betta_0 (saved by Fritzing 0.7.12b)
breadboards: 1

parts:
  U1 = attiny85 [package=dip]
  Q1 = NPN-Transistor [package="TO92 [THT]"]
  Q2 = NPN-Transistor [package="TO92 [THT]"]
  Q3 = NPN-Transistor [package="TO92 [THT]"]
  Q4 = NPN-Transistor [package="TO92 [THT]"]
  Q5 = PNP-Transistor [package="TO92 [THT]"]
  S1 = Pushbutton [package="[THT]"]
  Y1 = Resonator [frequency="16 Mhz" package=THT]
  C2 = Electrolytic Capacitor [capacitance=100µ package="100 mil [THT, electrolytic]"]
  LED1 = LED - 5mm [color="Red (633nm)" package="5 mm [THT]"]
  C3 = Ceramic Capacitor [capacitance=330nF package="0805 [SMD, multilayer]"]
  LED2 = LED - 5mm [color="Infrared (940nm)" package="5 mm [THT]"]
  LED3 = LED - 5mm [color="Infrared (940nm)" package="5 mm [THT]"]
  LED4 = LED - 5mm [color="Infrared (940nm)" package="5 mm [THT]"]
  LED5 = LED - 5mm [color="Infrared (940nm)" package="5 mm [THT]"]
  S2 = Toggle Switch [package=THT]
  VCC1 = Battery block 9V
  U2 = Voltage Regulator - 5V [package="DPak [SMD]"]
  R4 = Resistor [tolerance=±5% resistance=1k package="1206 [SMD]"]
  C1 = Ceramic Capacitor [capacitance=100nF package="0805 [SMD, multilayer]"]
  R3 = Resistor [tolerance=±5% resistance=10k package="1206 [SMD]"]
  R2 = Resistor [tolerance=±5% resistance=10k package="1206 [SMD]"]
  R1 = Resistor [tolerance=±5% resistance=1k package="1206 [SMD]"]

nets:
  N1: U1.Pin_1, S1.Pin_1, S1.Pin_2
  N2: U1.Pin_2, Y1.0
  N3: U1.Pin_3, Y1.pin_1
  GND: U1.Pin_4, Q1.E, Q2.E, Q3.E, Q4.E, S1.Pin_3, S1.Pin_4, Y1.GND, C2.-, C3.0, VCC1.-, U2.GND, C1.0, R3.Pin_1, R2.Pin_1
  N4: U1.Pin_5, R1.Pin_0
  N5: U1.Pin_6, R4.Pin_0
  N6: U1.Pin_7, R3.Pin_0
  5V: U1.Pin_8, Q5.E, C2.+, LED1.anode, LED2.anode, LED3.anode, LED4.anode, LED5.anode, U2.output_voltage, C1.1
  N7: Q1.B, Q2.B, Q3.B, Q4.B, Q5.C, R2.Pin_0
  N8: Q1.C, LED2.cathode
  N9: Q2.C, LED3.cathode
  N10: Q3.C, LED4.cathode
  N11: Q4.C, LED5.cathode
  N12: Q5.B, R1.Pin_1
  N13: LED1.cathode, R4.Pin_1
  9V: C3.1, S2.L1, U2.input_voltage
  N14: S2.COM, VCC1.+
