# Fritzing sketch id4291_TVlights_0 (saved by Fritzing 0.8.7b)
breadboards: 2

parts:
  Part1 = Arduino Uno (Rev3)
  Q1 = npn-Powertransistor [package="TO220 [THT]"]
  Q2 = npn-Powertransistor [package="TO220 [THT]"]
  Q3 = npn-Powertransistor [package="TO220 [THT]"]
  R1 = Rotary Potentiometer (Small) [maximum_resistance=100kΩ package=THT]
  S1 = Pushbutton [package="[THT]"]
  R2 = Resistor [tolerance=±5% resistance=220 package=THT]
  R3 = Resistor [tolerance=±5% resistance=220 package=THT]
  LED1 = LED Strip
  LED2 = LED Strip
  LED3 = LED Strip
  LED4 = LED Strip
  R4 = Resistor [tolerance=±5% resistance=220 package=THT]
  R5 = Resistor [tolerance=±5% resistance=220 package=THT]

nets:
  N1: Part1.A0, R1.wiper
  N2: Part1.D2, S1.Pin_3, S1.Pin_4, R5.Pin_0
  N3: Part1.D3_PWM, R2.Pin_1
  N4: Part1.D5_PWM, R3.Pin_1
  N5: Part1.D6_PWM, R4.Pin_1
  N6: Part1.5V, R1.leg1, R5.Pin_1
  N7: Part1.GND, Q1.emitter, Q2.emitter, Q3.emitter, R1.leg2, S1.Pin_2
  N8: Part1.VIN, LED1.connector1, LED2.connector1, LED3.connector1, LED4.connector1
  N9: Q1.base, R2.Pin_0
  N10: Q1.collector, LED1.connector0, LED2.connector0, LED3.connector0, LED4.connector0
  N11: Q2.base, R4.Pin_0
  N12: Q2.collector, LED1.connector2, LED2.connector2, LED3.connector2, LED4.connector2
  N13: Q3.base, R3.Pin_0
  N14: Q3.collector, LED1.connector3, LED2.connector3, LED3.connector3, LED4.connector3

notes:
  VIN is 12v
