# Fritzing sketch id4292_TVPLATFORM_FRITZ_0 (saved by Fritzing 0.9.3b)
breadboards: 1

parts:
  Part1 = Arduino Mega 2560 (Rev3)
  U1 = SLIDER [package=slider]
  U2 = SLIDER [package=slider]
  U3 = SLIDER [package=slider]
  U4 = POT [package=pot_alpha_rv16af-20]
  U5 = POT [package=pot_alpha_rv16af-20]
  SP1 = SPEAKER [package=pcb_mount_speaker]
  300_ohm = Resistor [tolerance=±5% resistance=220 package="0805 [SMD]"]
  To_VCC = RELAY [package=relay-g5q]  # not connected
  U7 = G3VM-61E1 [package=g3vm-61e1]
  U8 = G3VM-61E1 [package=g3vm-61e1]
  U9 = G3VM-61E1 [package=g3vm-61e1]
  U10 = G3VM-61E1 [package=g3vm-61e1]
  U11 = G3VM-61E1 [package=g3vm-61e1]
  U12 = G3VM-61E1 [package=g3vm-61e1]
  U13 = G3VM-61E1 [package=g3vm-61e1]
  To_VCC_2 = G3VM-61E1 [package=g3vm-61e1]
  U15 = prefix0000
  U16 = prefix0000
  HLK-PM1 = HLK-PM01
  M1 = DC Motor
  U17 = RF-LINK_RX [package=rf-link_rx]

nets:
  N1: Part1.A1, U1.S
  N2: Part1.A2, U2.S
  N3: Part1.A3, U3.S
  N4: Part1.A4, U4.S
  N5: Part1.A5, U5.S
  N6: Part1.D12_PWM, U16.connector4
  N7: Part1.D11_PWM, U15.connector4
  N8: Part1.D10_PWM, U13.P$5
  N9: Part1.D9_PWM, U12.P$5
  N10: Part1.D8_PWM, U11.P$5, U11.P$6
  N11: Part1.5V, U1.E, U3.E, U4.A, U5.A, To_VCC_2.P$6
  N12: Part1.GND, U1.A, U2.A, U3.A, U4.E, U5.E, SP1.+, U12.P$3, U17.ANT
  N13: Part1.D3_PWM, U7.P$5
  N14: Part1.D4_PWM, To_VCC_2.P$5
  N15: Part1.D5_PWM, U8.P$5
  N16: Part1.D6_PWM, U9.P$5
  N17: Part1.D7_PWM, U10.P$5
  N18: Part1.D22, SP1.-, 300_ohm.Pin_0, 300_ohm.Pin_1
  N19: U12.P$2, M1.pin_2
  N20: U13.P$1, HLK-PM1.-Vo
  N21: U13.P$2, M1.pin_1
  N22: U13.P$3, HLK-PM1.+Vo

notes:
  To Ground]
  additional 3 motors wired as to the right
  One additional motor
