# Fritzing sketch id4293_twelite_button_0 (saved by Fritzing 0.9.2b)
breadboards: 1

parts:
  パーツ1 = TWE-LITE DIP [chip_label="TWE-LITE DIP"]
  R1 = Resistor [tolerance=±0.05% resistance=1M package=THT]
  U1 = TC7SU04F [package=sot23-5]
  R2 = Resistor [tolerance=±0.05% resistance=1M package=THT]
  U2 = Vibration Motor- ROB-08449 [package=vibe-motor-10mm]
  LED1 = LEDs [package=led10mm]
  R4 = Resistor [tolerance=±5% resistance=47 package=THT]
  LED3 = LEDs [package=led10mm]
  BAT1 = Battery Holders [package=battcom_20mm_pth]
  S2 = Round Pushbutton
  R3 = Resistor [tolerance=±0.05% resistance=1M package=THT]
  R3_2 = Resistor [tolerance=±5% resistance=47 package=THT]

nets:
  N1: パーツ1.connector0, パーツ1.connector12, パーツ1.connector25, パーツ1.connector26, R1.Pin_0, U1.GND, R2.Pin_0, U2.+, LED1.C, BAT1.-
  N2: パーツ1.connector14, R1.Pin_1, U1.IN, U2.-, S2.leg0, R3.Pin_0, R3_2.Pin_0
  N3: パーツ1.connector15, U1.OUT, U1.+V, R2.Pin_1
  N4: パーツ1.connector27, U1.NC, R4.Pin_1, BAT1.+, S2.leg1
  N5: LED1.A, R3.Pin_1, R3_2.Pin_1
  N6: R4.Pin_0, LED3.A
