# Fritzing sketch id4294_Twins_Chip_Mini_Radar_0 (saved by Fritzing 0.9.0b)

parts:
  Part1 = Arduino Uno (Rev3)
  J1 = Basic Servo
  J4 = Screw terminal - 2 pins [package=THT]
  J5 = Screw terminal - 2 pins [package=THT]

nets:
  N1: Part1.D2, J4.pin1
  N2: Part1.D3_PWM, J5.pin2
  N3: Part1.D4, J1.pulse
  N4: Part1.5V, J5.pin1
  GND: Part1.GND, J1.gnd, J4.pin2
  VIN: Part1.VIN, J1.vcc

notes:
  Ultrasonic Sensor
  HC-SR04
  1 VCC
  2 TRIG
  3 ECHO
  4 GND
  Power Pin for Servo
  Vin = 9V
