# Fritzing sketch id4295_Weather_Station_0 (saved by Fritzing 0.9.2b)
circuit board: 8.46667cm x 5.64444cm
breadboards: 1
perfboards: 1

parts:
  Part1 = Intel Edison Arduinobreakout
  MQ2 = GAS_SENSOR [package=mq-3]
  SL-HS-1 = humiditySLHS220
  R1 = Temperature Sensor (Thermistor) [thermistor_type=NTC package=THT]
  IC1 = IC, DIP package, 6 pins [chip_label=ADC]
  R2 = Resistor [tolerance=±5% resistance=220 package="1206 [SMD]"]
  R3 = Resistor [tolerance=±5% resistance=220 package="1206 [SMD]"]

nets:
  N1: Part1.A0, R1.pin_1, R2.Pin_0
  N2: Part1.A1, SL-HS-1.connector9
  N3: Part1.A2, MQ2.H1, R3.Pin_0
  N4: Part1.D2, IC1.pin3
  N5: Part1.5V, MQ2.B1, SL-HS-1.connector11, R1.pin_0, IC1.pin1
  N6: Part1.GND, MQ2.A1, SL-HS-1.connector10, IC1.pin2, R2.Pin_1, R3.Pin_1

notes:
  Rain Sensor
  i/p1
  i/p2
