# Fritzing sketch id4296_Two_Buttons_Two_Leds___Week_3_0 (saved by Fritzing 0.9.3b)
circuit board: 6.88566cm x 5.36311cm
breadboards: 1

parts:
  Arduino1 = Arduino Uno (Rev3)
  R1 = Resistor [tolerance=±5% resistance=10k package=THT]
  R2 = Resistor [tolerance=±20% resistance=220 package=THT]
  S3 = Pushbutton [package="[THT]"]
  R3 = Resistor [tolerance=±5% resistance=10k package=THT]
  S4 = Pushbutton [package="[THT]"]
  LED1 = LED - 5mm [color="Red (633nm)" package="5 mm [THT]"]
  LED2 = LED - 5mm [color="Red (633nm)" package="5 mm [THT]"]

nets:
  N1: Arduino1.D11_PWM/MOSI, LED1.anode
  N2: Arduino1.D13/SCK, LED2.anode
  N3: Arduino1.GND, R1.Pin_1, R2.Pin_1, R3.Pin_1, LED2.cathode
  N4: Arduino1.D2, S3.Pin_1, S3.Pin_2, R3.Pin_0
  N5: Arduino1.D3_PWM, R1.Pin_0, S4.Pin_1, S4.Pin_2
  N6: Arduino1.5V, S3.Pin_3, S3.Pin_4, S4.Pin_3, S4.Pin_4
  N7: R2.Pin_0, LED1.cathode

notes:
  Color code for brown resistors:
  220 ohm: red, red, brown, gold
  10K ohm: brown, black, orange, gold
  220 ohm resistor for LED
  10K ohm for button
