# Fritzing sketch id4298_motor2_0 (saved by Fritzing 0.9.2b)
breadboards: 1

parts:
  IC1 = L293D [package=THT]
  L1 = Solenoid
  Raspberry_Pi1 = Raspberry Pi 2
  VCC1 = 4 x AAA Battery Mount
  L2 = Solenoid

nets:
  N1: IC1.Enable_1, Raspberry_Pi1.GPIO18
  N2: IC1.In_1, Raspberry_Pi1.GPIO23
  N3: IC1.Out_1_(_Controlled_by_Enable_1_), L1.pin2
  N4: IC1.0V, Raspberry_Pi1.GND, VCC1.-
  N5: IC1.Out_2_(_Controlled_by_Enable_1_), L1.pin1
  N6: IC1.In_2, Raspberry_Pi1.GPIO24
  N7: IC1.+Vmotor, VCC1.+
  N8: IC1.Enable_2, Raspberry_Pi1.GPIO12
  N9: IC1.In_3, Raspberry_Pi1.GPIO20
  N10: IC1.Out_3_(_Controlled_by_Enable_2_), L2.pin2
  N11: IC1.Out_4_(_Controlled_by_Enable_2_), L2.pin1
  N12: IC1.In_4, Raspberry_Pi1.GPIO16
  N13: IC1.+V, Raspberry_Pi1.5V
