# Fritzing sketch id4299_Mini_Golf_Vote_Counter_0 (saved by Fritzing 0.9.3b)
breadboards: 1

parts:
  Part1 = Arduino Uno (Rev3)
  Part2 = SRF05 Ultrasonic Rangefinder
  Part3 = SRF05 Ultrasonic Rangefinder
  LCD1 = LCD screen
  R1 = Rotary Potentiometer (Small) [maximum_resistance=100kΩ package=THT]

nets:
  N1: Part1.D8, LCD1.E
  N2: Part1.D9_PWM, LCD1.DB4
  N3: Part1.D10_PWM/SS, LCD1.DB5
  N4: Part1.D11_PWM/MOSI, LCD1.DB6
  N5: Part1.D12/MISO, LCD1.DB7
  GND: Part1.GND, Part2.connector11, Part3.connector11, LCD1.VSS, LCD1.R/W, R1.leg2
  N6: Part1.D2, Part3.connector10
  N7: Part1.D3_PWM, Part3.connector9
  N8: Part1.D4, Part2.connector9
  N9: Part1.D5_PWM, Part2.connector10
  N10: Part1.D7, LCD1.RS
  5V: Part1.5V, Part2.connector8, Part3.connector8, LCD1.VDD, R1.leg1
  N11: LCD1.V0, R1.wiper

notes:
  Note: This project uses a 20x4 LCD. Circuit is the same.
