# Fritzing sketch id42_16leds_0 (saved by Fritzing 0.4.3b)
breadboards: 1

parts:
  R1 = Resistor [resistance=120 package=THT]
  R2 = Resistor [resistance=120 package=THT]
  R3 = Resistor [resistance=120 package=THT]
  R4 = Resistor [resistance=120 package=THT]
  R5 = Resistor [resistance=120 package=THT]
  R6 = Resistor [resistance=120 package=THT]
  R7 = Resistor [resistance=120 package=THT]
  R8 = Resistor [resistance=120 package=THT]
  R9 = Resistor [resistance=120 package=THT]
  R10 = Resistor [resistance=120 package=THT]
  R11 = Resistor [resistance=120 package=THT]
  R12 = Resistor [resistance=120 package=THT]
  R13 = Resistor [resistance=120 package=THT]
  R14 = Resistor [resistance=120 package=THT]
  R15 = Resistor [resistance=120 package=THT]
  R16 = Resistor [resistance=120 package=THT]
  LED1 = Red LED - 5mm
  LED2 = Red LED - 5mm
  LED3 = Red LED - 5mm
  LED4 = Red LED - 5mm
  LED5 = Red LED - 5mm
  LED6 = Red LED - 5mm
  LED7 = Red LED - 5mm
  LED8 = Red LED - 5mm
  LED9 = Red LED - 5mm
  LED10 = Red LED - 5mm
  LED11 = Red LED - 5mm
  LED12 = Red LED - 5mm
  LED13 = Red LED - 5mm
  LED14 = Red LED - 5mm
  LED15 = Red LED - 5mm
  LED16 = Red LED - 5mm
  IC4 = IC, DIP package, 24 pins [chip_label=IC spacing=300mil]
  Arduino1 = Arduino
  R17 = Resistor [resistance=4.7k package=THT]
  R18 = Resistor [resistance=4.7k package=THT]

nets:
  N1: R1.Pin_0, LED16.anode
  N2: R1.Pin_1, R2.Pin_1, R3.Pin_1, R4.Pin_1, R5.Pin_1, R6.Pin_1, R7.Pin_1, R8.Pin_1, R9.Pin_1, R10.Pin_1, R11.Pin_1, R12.Pin_1, R13.Pin_1, R14.Pin_1, R15.Pin_1, R16.Pin_1, IC4.pin24, Arduino1.+5V, R17.Pin_1, R18.Pin_1
  N3: R2.Pin_0, LED10.anode
  N4: R3.Pin_0, LED11.anode
  N5: R4.Pin_0, LED15.anode
  N6: R5.Pin_0, LED14.anode
  N7: R6.Pin_0, LED12.anode
  N8: R7.Pin_0, LED13.anode
  N9: R8.Pin_0, LED1.anode
  N10: R9.Pin_0, LED2.anode
  N11: R10.Pin_0, LED4.anode
  N12: R11.Pin_0, LED3.anode
  N13: R12.Pin_0, LED5.anode
  N14: R13.Pin_0, LED6.anode
  N15: R14.Pin_0, LED7.anode
  N16: R15.Pin_0, LED8.anode
  N17: R16.Pin_0, LED9.anode
  N18: LED1.cathode, IC4.pin4
  N19: LED2.cathode, IC4.pin5
  N20: LED3.cathode, IC4.pin6
  N21: LED4.cathode, IC4.pin7
  N22: LED5.cathode, IC4.pin8
  N23: LED6.cathode, IC4.pin9
  N24: LED7.cathode, IC4.pin10
  N25: LED8.cathode, IC4.pin11
  N26: LED9.cathode, IC4.pin13
  N27: LED10.cathode, IC4.pin14
  N28: LED11.cathode, IC4.pin15
  N29: LED12.cathode, IC4.pin16
  N30: LED13.cathode, IC4.pin17
  N31: LED14.cathode, IC4.pin18
  N32: LED15.cathode, IC4.pin19
  N33: LED16.cathode, IC4.pin20
  N34: IC4.pin12, Arduino1.GND
  N35: IC4.pin22, Arduino1.A5, R17.Pin_0
  N36: IC4.pin23, Arduino1.A4, R18.Pin_0

notes:
  IC is PCA9555
