# Fritzing sketch id4300_two_servo_0 (saved by Fritzing 0.7.10b)
breadboards: 1

parts:
  Arduino1 = Arduino
  J1 = Basic Servo
  J2 = Basic Servo
  DC_Power1 = DC Power [voltage=5]  # not connected

nets:
  GND: Arduino1.GND, J1.gnd, J2.gnd
  N1: Arduino1.D9, J2.pulse
  VCC: J1.vcc, J2.vcc
