# Fritzing sketch id4301_PING_SONAR_RELAY_0 (saved by Fritzing 0.9.2b)
breadboards: 1

parts:
  Part1 = Arduino Uno (Rev3)
  Transistor = NPN-Transistor [part_number=P2N2222A package="TO92 [THT]"]
  R1 = Resistor [tolerance=±5% resistance=330 package=THT]
  Relay = RELAY [package=relay-jzc]
  Diode = Diode [package=diode-1n4001]

nets:
  N1: Part1.D2, R1.Pin_1
  N2: Part1.GND, Transistor.E
  N3: Transistor.B, R1.Pin_0
  N4: Transistor.C, Relay.COIL2, Diode.A
  N5: Relay.COIL1, Diode.C

notes:
  This is designed for a 4s pin Ultrasonic Sensor PING.
  This box represents a SONAR SENSOR #1 (may be the front one on the Go Kart).
  Blue is GND;
  Orange is VCC;
  Red is pin #8 Trig
  Yellow is ECHO pin # 7
  The ground is Blue and 5V is red color
  See Circuit 11 for the relay set up
  Goes to positice of the high power
  The the high load such a DC motor
  This is designed for a 4s pin Ultrasonic Sensor PING.
  This box represents a SONAR SENSOR #1 (may be the front one on the Go Kart).
  Blue is GND;
  Orange is VCC;
  White is pin #12 Trig
  Yellow is ECHO pin # 13
