# Fritzing sketch id4302_TwoWayLevelShifter_0 (saved by Fritzing 0.9.1b)
circuit board: 1.36991cm x 2.679cm
breadboards: 1

parts:
  Q1 = NPN-Transistor [package="TO92 [THT]"]
  Q2 = NPN-Transistor [package="TO92 [THT]"]
  V+ = Resistor [tolerance=±5% resistance=220 package=THT]
  V++ = Resistor [tolerance=±5% resistance=220 package=THT]
  2WayLevelShifter = Resistor [tolerance=±5% resistance=220 package=THT]
  J1 = female pin header, 2 pins [form="♀ (female)"]
  J2 = female pin header, 2 pins [form="♀ (female)"]
  EN = female pin header, 2 pins [form="♀ (female)"]

nets:
  N1: Q1.E, Q2.C, V++.Pin_1, J2.pin2
  N2: Q1.B, Q2.B, 2WayLevelShifter.Pin_0
  N3: Q1.C, Q2.E, V+.Pin_0, J1.pin1
  N4: V+.Pin_1, J1.pin2, EN.pin2
  N5: V++.Pin_0, J2.pin1
  N6: 2WayLevelShifter.Pin_1, EN.pin1
