# Fritzing sketch id4303_tzone_machine_schema_0 (saved by Fritzing 0.9.3b)
breadboards: 1

parts:
  Part1 = Arduino Uno (Rev3) - ICSP
  IC1 = L293D [package=THT]
  M1 = DC Motor  # not connected
  M2 = DC Motor  # not connected

nets:
  N1: Part1.D6_PWM, IC1.In_2
  N2: IC1.Enable_1, IC1.+Vmotor, IC1.+V
