# Fritzing sketch id4305_Sketch_U1_0 (saved by Fritzing 0.9.3b)
breadboards: 1

parts:
  Часть1 = Arduino Micro (Rev3)
  R1 = Resistor [tolerance=±5% resistance=220 package=THT]
  R2 = Resistor [tolerance=±5% resistance=220 package=THT]
  LED2 = LED - 5mm [color="Blue (470nm)" package="5 mm [THT]"]
  Часть2 = Bluetooth HC-05 Macho
  hc-sr1 = hc-sr04
  LED3 = LED - 5mm [color="Red (633nm)" package="5 mm [THT]"]

nets:
  GND: Часть1.GND, LED2.cathode, Часть2.GND, hc-sr1.GND, LED3.anode
  N1: Часть1.D4_PWM/A6, Часть2.TXD
  N2: Часть1.D5_PWM, Часть2.RXD
  N3: Часть1.D6_PWM/A7, hc-sr1.Trig
  N4: Часть1.D7, hc-sr1.Echo
  VCC: Часть1.VIN, Часть2.VCC, hc-sr1.VCC
  N5: Часть1.A2, Часть2.State
  N6: Часть1.A1, R2.Pin_0
  N7: Часть1.A0, R1.Pin_0
  N8: R1.Pin_1, LED2.anode
  N9: R2.Pin_1, LED3.cathode
