# Fritzing sketch id4306_Servo_Shield_1_Layer_0 (saved by Fritzing 0.9.2b)
circuit board: 6.9215cm x 5.33756cm
breadboards: 1

parts:
  P1 = female pin header, 3 pins [form="♀ (female)"]
  P2 = female pin header, 3 pins [form="♀ (female)"]
  P3 = female pin header, 3 pins [form="♀ (female)"]
  P4 = female pin header, 3 pins [form="♀ (female)"]
  P5 = female pin header, 3 pins [form="♀ (female)"]
  P6 = female pin header, 3 pins [form="♀ (female)"]
  GND_5V_3V3_12V = screw terminal, 4 pins
  S6 = Basic Servo
  S5 = Basic Servo
  S4 = Basic Servo
  S3 = Basic Servo
  S2 = Basic Servo
  S1 = Basic Servo
  270Ω = Resistor [tolerance=±5% resistance=270 package=THT]
  Notaus = LED - 5mm [color="Red (633nm)" package="5 mm [THT]"]
  Notaus_2 = Pushbutton [package="[THT]"]
  Servoshield_UARM_v1_0 = Arduino Uno (Rev3)

nets:
  N1: P1.pin1, P2.pin1, P3.pin1, P4.pin1, P5.pin1, P6.pin1, Servoshield_UARM_v1_0.5V
  N2: P1.pin2, Servoshield_UARM_v1_0.A0
  GND: P1.pin3, P2.pin3, P3.pin3, P4.pin3, P5.pin3, P6.pin3, GND_5V_3V3_12V.pin4, S6.gnd, S5.gnd, S4.gnd, S3.gnd, S2.gnd, S1.gnd, Notaus.cathode, Notaus_2.Pin_1, Notaus_2.Pin_2, Servoshield_UARM_v1_0.GND
  N3: P2.pin2, Servoshield_UARM_v1_0.A1
  N4: P3.pin2, Servoshield_UARM_v1_0.A2
  N5: P4.pin2, Servoshield_UARM_v1_0.A3
  N6: P5.pin2, Servoshield_UARM_v1_0.A4/SDA
  N7: P6.pin2, Servoshield_UARM_v1_0.A5/SCL
  VCC: GND_5V_3V3_12V.pin3, S6.vcc, S5.vcc, S4.vcc, S3.vcc, S2.vcc, S1.vcc
  N8: S6.pulse, Servoshield_UARM_v1_0.D11_PWM/MOSI
  N9: S5.pulse, Servoshield_UARM_v1_0.D10_PWM/SS
  N10: S4.pulse, Servoshield_UARM_v1_0.D9_PWM
  N11: S3.pulse, Servoshield_UARM_v1_0.D6_PWM
  N12: S2.pulse, Servoshield_UARM_v1_0.D5_PWM
  N13: S1.pulse, Servoshield_UARM_v1_0.D3_PWM
  N14: 270Ω.Pin_0, Servoshield_UARM_v1_0.D13/SCK
  N15: 270Ω.Pin_1, Notaus.anode
  N16: Notaus_2.Pin_3, Notaus_2.Pin_4, Servoshield_UARM_v1_0.D2

notes:
  made by S. Gleis
  Aduino Uno
  S. Gleis
  12V
  3V3
  5V
  GND
