# Fritzing sketch id4307_Servo_Shield_2_Layer_0 (saved by Fritzing 0.9.2b)
circuit board: 6.9215cm x 5.33756cm
breadboards: 1

parts:
  Servoshield_UARM_v_1 = Arduino Uno (Rev3)
  P1 = female pin header, 3 pins [form="♀ (female)"]
  P2 = female pin header, 3 pins [form="♀ (female)"]
  P3 = female pin header, 3 pins [form="♀ (female)"]
  P4 = female pin header, 3 pins [form="♀ (female)"]
  P5 = female pin header, 3 pins [form="♀ (female)"]
  P6 = female pin header, 3 pins [form="♀ (female)"]
  GND_5V_3V3_12V = screw terminal, 4 pins
  S6 = Basic Servo
  S5 = Basic Servo
  S4 = Basic Servo
  S3 = Basic Servo
  S2 = Basic Servo
  S1 = Basic Servo
  Notaus = Pushbutton [package="[THT]"]
  270Ω = Resistor [tolerance=±5% resistance=270 package=THT]
  Notaus_2 = LED - 5mm [color="Red (633nm)" package="5 mm [THT]"]

nets:
  N1: Servoshield_UARM_v_1.A0, P1.pin2
  N2: Servoshield_UARM_v_1.A1, P2.pin2
  N3: Servoshield_UARM_v_1.A2, P3.pin2
  N4: Servoshield_UARM_v_1.A3, P4.pin2
  N5: Servoshield_UARM_v_1.A4/SDA, P5.pin2
  N6: Servoshield_UARM_v_1.A5/SCL, P6.pin2
  N7: Servoshield_UARM_v_1.D9_PWM, S4.pulse
  N8: Servoshield_UARM_v_1.D10_PWM/SS, S5.pulse
  N9: Servoshield_UARM_v_1.D11_PWM/MOSI, S6.pulse
  N10: Servoshield_UARM_v_1.D13/SCK, 270Ω.Pin_0
  GND: Servoshield_UARM_v_1.GND, P1.pin3, P2.pin3, P3.pin3, P4.pin3, P5.pin3, P6.pin3, GND_5V_3V3_12V.pin4, S6.gnd, S5.gnd, S4.gnd, S3.gnd, S2.gnd, S1.gnd, Notaus.Pin_1, Notaus.Pin_2, Notaus_2.cathode
  N11: Servoshield_UARM_v_1.D2, Notaus.Pin_3, Notaus.Pin_4
  N12: Servoshield_UARM_v_1.D3_PWM, S1.pulse
  N13: Servoshield_UARM_v_1.D5_PWM, S2.pulse
  N14: Servoshield_UARM_v_1.D6_PWM, S3.pulse
  N15: Servoshield_UARM_v_1.5V, P1.pin1, P2.pin1, P3.pin1, P4.pin1, P5.pin1, P6.pin1
  VCC: GND_5V_3V3_12V.pin3, S6.vcc, S5.vcc, S4.vcc, S3.vcc, S2.vcc, S1.vcc
  N16: 270Ω.Pin_1, Notaus_2.anode

notes:
  made by S. Gleis
  Aduino Uno
  S. Gleis
  12V
  3V3
  5V
  GND
