# Fritzing sketch id4308_traffic_v1_0 (saved by Fritzing 0.9.0b)
breadboards: 1

parts:
  Dels_Arduino_Sandbox = Arduino Uno (Rev3)
  LED1 = LED - 5mm [color="Red (633nm)" package="5 mm [THT]"]
  R1 = Resistor [tolerance=±5% resistance=1.5k package=THT]
  LED2 = LED - 5mm [color="Yellow (595nm)" package="5 mm [THT]"]
  R2 = Resistor [tolerance=±5% resistance=220 package=THT]
  LED3 = LED - 5mm [color="Green (570nm)" package="5 mm [THT]"]
  R3 = Resistor [tolerance=±5% resistance=220 package=THT]

nets:
  N1: Dels_Arduino_Sandbox.D8, R2.Pin_1
  N2: Dels_Arduino_Sandbox.D9_PWM, R3.Pin_1
  N3: Dels_Arduino_Sandbox.GND, LED1.cathode, LED2.cathode, LED3.cathode
  N4: Dels_Arduino_Sandbox.D7, R1.Pin_1
  N5: LED1.anode, R1.Pin_0
  N6: LED2.anode, R2.Pin_0
  N7: LED3.anode, R3.Pin_0

notes:
  Traffic Light Setup
  Using PIN7, 8, & 9
