# Fritzing sketch id4309_UKW_Radio_0 (saved by Fritzing 0.9.3b)
circuit board: 9cm x 5cm
perfboards: 1

parts:
  U1 = LM386 [part_number=2 package=dip08]
  IC2 = Voltage Regulator [part_number=3 package=to-92]
  R1 = Resistor [tolerance=±5% resistance=1k package=THT]
  R3 = Resistor [tolerance=±5% resistance=10k package=THT]
  R4 = Resistor [tolerance=±5% resistance=220k package=THT]
  C1 = Ceramic Capacitor [capacitance=100nF package="100 mil [THT, multilayer]"]
  C2 = Electrolytic Capacitor [capacitance=100µF voltage=35V package="300 mil [THT, electrolytic]"]
  C3 = Electrolytic Capacitor [capacitance=100µF voltage=35V package="300 mil [THT, electrolytic]"]
  IC1 = IC, SIP package, 6 pins [chip_label="TDA 7088"]
  S1 = Pushbutton [package=THT]
  J1 = Screw terminal - 2 pins [package=THT]
  J2 = Screw terminal - 2 pins [package=THT]
  J3 = Screw terminal - 2 pins [package=THT]
  R2 = Rotary Potentiometer (Large) [maximum_resistance=100kΩ package=THT]
  R7 = Rotary Potentiometer (Large) [maximum_resistance=100kΩ package=THT]

nets:
  N1: U1.-IN, C1.1
  N2: U1.V-, IC2.GND, R3.Pin_1, C2.-, IC1.pin5, S1.leg0, J2.pin2, J3.pin2, R7.leg1
  N3: U1.OUT, C3.+
  N4: U1.V+, IC2.IN, C2.+, J1.pin1
  N5: IC2.OUT, R1.Pin_1, IC1.pin2
  N6: R1.Pin_0, R2.leg2
  N7: R3.Pin_0, R2.leg1
  N8: R4.Pin_0, IC1.pin4
  N9: R4.Pin_1, R2.wiper
  N10: C1.0, R7.wiper
  N11: C3.-, J2.pin1
  N12: IC1.pin1, J3.pin1
  N13: IC1.pin6, R7.leg2
  N14: S1.leg1, J1.pin2

notes:
  DC 9V
  Antenne
