# Fritzing sketch id430_Arduino_Burgaler_Alarm_0 (saved by Fritzing 0.9.1b)
breadboards: 1

parts:
  Arduino = Arduino Uno (Rev3)
  RFID_Receiver = rc522
  PIR_Sensor = PIR_sensor
  Piezo_Buzzer = Piezo Speaker
  Enabled_LED = LED - 5mm [color="Red (633nm)" package="5 mm [THT]"]
  Motion_LED = LED - 5mm [color="Red (633nm)" package="5 mm [THT]"]
  R1 = Resistor [tolerance=±5% resistance=220 package=THT]
  R2 = Resistor [tolerance=±5% resistance=220 package=THT]

nets:
  N1: Arduino.D9_PWM, RFID_Receiver.connector14
  N2: Arduino.D10_PWM/SS, RFID_Receiver.connector8
  N3: Arduino.D11_PWM/MOSI, RFID_Receiver.connector10
  N4: Arduino.D12/MISO, RFID_Receiver.connector11
  N5: Arduino.D13/SCK, RFID_Receiver.connector9
  N6: Arduino.D2, PIR_Sensor.connector2
  N7: Arduino.D5_PWM, Piezo_Buzzer.pin2
  N8: Arduino.D6_PWM, Motion_LED.anode
  N9: Arduino.D7, Enabled_LED.anode
  N10: Arduino.5V, RFID_Receiver.connector15, PIR_Sensor.connector1
  N11: Arduino.GND, RFID_Receiver.connector13, PIR_Sensor.connector3, Piezo_Buzzer.pin1, R1.Pin_1, R2.Pin_1
  N12: Enabled_LED.cathode, R1.Pin_0
  N13: Motion_LED.cathode, R2.Pin_0

notes:
  RFID Receiver is not the same as I used but it is similar.
