# Fritzing sketch id4311_ULN2003A_0 (saved by Fritzing 0.8.7b)
circuit board: 10.16cm x 5.36194cm
breadboards: 1

parts:
  IC1 = ULN2003A [package="SO16 [SMD]"]
  IC2 = ULN2003A [package="SO16 [SMD]"]
  Part1 = Arduino Mega ADK (Rev3)
  IC3 = ULN2003A [package="SO16 [SMD]"]
  JP1 = Header 12 [package=1x12_machine-pin-header_lock.004]
  JP2 = Header 12 [package=1x12_machine-pin-header_lock.004]
  JP6 = Header 1 [package=pad-1.5x4.5]
  JP7 = Header 1 [package=pad-1.5x4.5]
  JP8 = Header 1 [package=pad-1.5x4.5]
  JP10 = Header 1 [package=pad-1.5x4.5]
  JP11 = Header 1 [package=pad-1.5x4.5]
  JP12 = Header 1 [package=pad-1.5x4.5]
  JP13 = Header 5x2 [package=2x5-raf]  # not connected
  JP14 = Header 5x2 [package=2x5-raf]  # not connected
  JP15 = Header 5x2 [package=2x5-raf]  # not connected
  JP16 = Header 5x2 [package=2x5-raf]  # not connected
  JP17 = Header 5x2 [package=2x5-raf]  # not connected
  JP18 = Header 5x2 [package=2x5-raf]  # not connected
  JP19 = Header 5x2 [package=2x5-raf]  # not connected
  JP20 = Header 5x2 [package=2x5-raf]  # not connected
  JP21 = Header 5x2 [package=2x5-raf]  # not connected
  JP22 = Header 5x2 [package=2x5-raf]  # not connected

nets:
  N1: IC1.In_1, Part1.D6_PWM
  N2: IC1.In_2, Part1.D5_PWM
  N3: IC1.In_3, Part1.D4_PWM
  N4: IC1.In_4, Part1.D3_PWM
  N5: IC1.In_5, Part1.D2_PWM
  N6: IC1.In_6, Part1.D1/TX0
  N7: IC1.In_7, Part1.D0/RX0
  N8: IC1.0V, IC2.0V, Part1.GND, IC3.0V, JP1.1, JP2.1, JP2.7
  N9: IC1.COM_-_Common, IC2.COM_-_Common, Part1.VIN, IC3.COM_-_Common
  N10: IC1.Out_7, JP2.8
  N11: IC1.Out_6, JP2.9
  N12: IC1.Out_5, JP2.10
  N13: IC1.Out_4, JP2.11
  N14: IC1.Out_3, JP6.1
  N15: IC1.Out_2, JP7.1
  N16: IC1.Out_1, JP8.1
  N17: IC2.In_1, Part1.D13_PWM
  N18: IC2.In_2, Part1.D12_PWM
  N19: IC2.In_3, Part1.D11_PWM
  N20: IC2.In_4, Part1.D10_PWM
  N21: IC2.In_5, Part1.D9_PWM
  N22: IC2.In_6, Part1.D8_PWM
  N23: IC2.In_7, Part1.D7_PWM
  N24: IC2.Out_7, JP1.2
  N25: IC2.Out_6, JP1.3
  N26: IC2.Out_5, JP1.4
  N27: IC2.Out_4, JP1.5
  N28: IC2.Out_3, JP1.6
  N29: IC2.Out_2, JP1.7
  N30: IC2.Out_1, JP1.8
  N31: Part1.D20/SDA, IC3.In_7
  N32: Part1.D19/RX1, IC3.In_6
  N33: Part1.D18/TX1, IC3.In_5
  N34: Part1.D17/RX2, IC3.In_4
  N35: Part1.D16/TX2, IC3.In_3
  N36: Part1.D15/RX3, IC3.In_2
  N37: Part1.D14/TX3, IC3.In_1
  N38: IC3.Out_7, JP2.2
  N39: IC3.Out_6, JP2.3
  N40: IC3.Out_5, JP2.4
  N41: IC3.Out_4, JP2.5
  N42: IC3.Out_3, JP12.1
  N43: IC3.Out_2, JP11.1
  N44: IC3.Out_1, JP10.1
