# Fritzing sketch id4312_Attiny85_Led_Flasher_v3_0 (saved by Fritzing 0.8.3b)
circuit board: 3.35462cm x 1.49919cm
breadboards: 1

parts:
  attiny85 = attiny85 [package=dip]
  R1 = Resistor [tolerance=±5% resistance=4.7k package=THT]
  LED1 = LED - 3mm [color="Green (560nm)" package="3 mm [THT]"]
  U1 = MCP1702
  C1 = Ceramic Capacitor [capacitance=1µF package="100 mil [THT, multilayer]"]
  C2 = Ceramic Capacitor [capacitance=1µF package="100 mil [THT, multilayer]"]
  +3V = female pin header, 1 pin [form="♀ (female)"]
  J1 = female pin header, 2 pins [form="♀ (female)"]
  GND = female pin header, 1 pin [form="♀ (female)"]

nets:
  GND: attiny85.Pin_4, LED1.cathode, U1.connector0, C1.0, C2.0, J1.pin2, GND.pin1
  N1: attiny85.Pin_6, R1.Pin_0
  N2: attiny85.Pin_8, U1.connector2, C2.1, +3V.pin1
  N3: R1.Pin_1, LED1.anode
  N4: U1.connector1, C1.1, J1.pin1

notes:
  ULP Led Flasher by Toggio 2013
  +12V
  GND
  www.arduinoelettronica.com
  +3V
