# Fritzing sketch id4313_Ultrasonic&Bluetooth_0 (saved by Fritzing 0.9.3b)

parts:
  Part1 = Arduino Uno (Rev3)
  Part2 = Bluetooth HC-05 Macho
  hc-sr1 = hc-sr04

nets:
  N1: Part1.D12/MISO, hc-sr1.Echo
  N2: Part1.D13/SCK, hc-sr1.Trig
  N3: Part1.D2, Part2.TXD
  N4: Part1.D3_PWM, Part2.RXD
  3V3: Part1.3V3, Part2.VCC
  5V: Part1.5V, hc-sr1.VCC
  GND: Part1.GND, Part2.GND, hc-sr1.GND
