# Fritzing sketch id4314_SmartFiets_0 (saved by Fritzing 0.9.0b)
breadboards: 1

parts:
  Onderdeel1 = SRF05 Ultrasonic Rangefinder
  Onderdeel2 = Arduino Uno (Rev3)
  LED5 = LED - 5mm [color="Red (633nm)" package="5 mm [THT]"]
  LED6 = LED - 5mm [color="Red (633nm)" package="5 mm [THT]"]
  LED7 = LED - 5mm [color="Green (565nm)" package="5 mm [THT]"]
  LED8 = LED - 5mm [color="Yellow (595nm)" package="5 mm [THT]"]
  LED10 = LED - 5mm [color="Green (565nm)" package="5 mm [THT]"]
  LED11 = LED - 5mm [color="Yellow (595nm)" package="5 mm [THT]"]
  R1 = Resistor [tolerance=±5% resistance=220 package=THT]
  R2 = Resistor [tolerance=±5% resistance=220 package=THT]
  R3 = Resistor [tolerance=±5% resistance=220 package=THT]
  R4 = Resistor [tolerance=±5% resistance=220 package=THT]
  R6 = Resistor [tolerance=±5% resistance=220 package=THT]
  R7 = Resistor [tolerance=±5% resistance=220 package=THT]

nets:
  N1: Onderdeel1.connector8, Onderdeel2.5V, R1.Pin_0, R2.Pin_0, R3.Pin_0, R4.Pin_0, R6.Pin_0, R7.Pin_0
  N2: Onderdeel1.connector11, Onderdeel2.GND
  N3: Onderdeel2.D8, LED5.anode
  N4: Onderdeel2.D9_PWM, LED6.anode
  N5: Onderdeel2.D10_PWM/SS, LED8.anode
  N6: Onderdeel2.D11_PWM/MOSI, LED11.anode
  N7: Onderdeel2.D12/MISO, LED7.anode
  N8: Onderdeel2.D13/SCK, LED10.anode
  N9: LED5.cathode, R1.Pin_1
  N10: LED6.cathode, R4.Pin_1
  N11: LED7.cathode, R2.Pin_1
  N12: LED8.cathode, R3.Pin_1
  N13: LED10.cathode, R6.Pin_1
  N14: LED11.cathode, R7.Pin_1
