# Fritzing sketch id4317_arduino_lamp_0 (saved by Fritzing 0.8.7b)
breadboards: 1

parts:
  Bauteil1 = Arduino Motor Shield (Rev3)
  Bauteil2 = Arduino Uno (Rev3)  # not connected
  S1 = Momentary Switch [package=ksa_sealed_tac_switch]  # not connected
  M1 = DC Motor  # not connected
  LED1 = LEDs [package=led10mm]
  R1 = Resistor [tolerance=±5% resistance=220 package=THT]
  J1 = Infrared Proximity Sensor

nets:
  N1: Bauteil1.D10_PWM, LED1.C
  N2: Bauteil1.D7, J1.Vout
  5V: Bauteil1.5V, J1.Vcc
  GND: Bauteil1.GND, R1.Pin_1, J1.GND
  N3: LED1.A, R1.Pin_0

notes:
  This is originally not build with an ir-distance-sensor, but an us-distance-sensor with tree pins.
  swith to implement an end swith later
