# Fritzing sketch id4318_Lcd_hc_s04_sensor_0 (saved by Fritzing 0.9.2b)
breadboards: 1

parts:
  J1 = Piezo Speaker
  Parte1 = Arduino Uno (Rev3)
  Parte2 = SRF05 Ultrasonic Rangefinder
  LCM1602_IIC1 = generic_ic_dip_22_300mil.fzp [part_number="LCM1602 IIC" chip_label="LCM1602 IIC"]

nets:
  N1: J1.pin2, Parte1.D9_PWM
  N2: Parte1.A4/SDA, LCM1602_IIC1.connector18
  N3: Parte1.A5/SCL, LCM1602_IIC1.connector19
  N4: Parte1.D11_PWM/MOSI, Parte2.connector10
  N5: Parte1.D12/MISO, Parte2.connector9
  N6: Parte1.5V, Parte2.connector8, LCM1602_IIC1.connector17
  N7: Parte1.GND, Parte2.connector11, LCM1602_IIC1.connector16
