# Fritzing sketch id4319_Ultrasonic_mapmaker_0 (saved by Fritzing 0.9.2b)
stripboards: 1

parts:
  HC-SR04 = SRF05 Ultrasonic Rangefinder
  C1 = Electrolytic Capacitor [capacitance=330µF voltage=20V package="100 mil [THT, electrolytic]"]
  Servo = Basic Servo
  Arduino_Mega = Arduino Mega 2560 (Rev3)

nets:
  VCC: HC-SR04.connector8, C1.+, Servo.vcc, Arduino_Mega.5V
  N1: HC-SR04.connector9, Arduino_Mega.D12_PWM
  N2: HC-SR04.connector10, Arduino_Mega.D11_PWM
  GND: HC-SR04.connector11, C1.-, Servo.gnd, Arduino_Mega.GND
  N3: Servo.pulse, Arduino_Mega.D9_PWM
