# Fritzing sketch id4321_TZ1 (saved by Fritzing 0.8.7b)
circuit board: 5.5cm x 3.3cm
breadboards: 1

parts:
  U1 = 555 Timer [package="DIP8 [THT]"]
  R1 = Resistor [tolerance=±5% resistance=220 package=THT]
  R2 = Resistor [tolerance=±5% resistance=220 package=THT]
  R3 = Resistor [tolerance=±5% resistance=220 package=THT]
  C1 = Ceramic Capacitor [capacitance=100nF package="100 mil [THT, multilayer]"]
  C2 = Ceramic Capacitor [capacitance=100nF package="100 mil [THT, multilayer]"]
  D1 = Rectifier Diode [part_number=1N4001 package="300 mil [THT]"]
  Q1 = npn-Powertransistor [package="TO220 [THT]"]
  VCC1 = Battery
  U2 = Transformer [package=transformer]
  D2 = Rectifier Diode [part_number=1N4001 package="300 mil [THT]"]

nets:
  N1: U1.Ground, C1.0, C2.0, Q1.emitter, VCC1.+, D2.anode
  N2: U1.Trigger, U1.Threshold, R1.Pin_1, C1.1
  N3: U1.Output, R2.Pin_0
  N4: U1.Reset, U1.Vcc_Supply_Voltage, R3.Pin_0, D1.cathode
  N5: U1.Control_Voltage, C2.1
  N6: U1.Discharge, R1.Pin_0, R3.Pin_1
  N7: R2.Pin_1, Q1.base
  N8: D1.anode, VCC1.-, U2.1
  N9: Q1.collector, U2.2, D2.cathode

notes:
  Wez 2014
