# Fritzing sketch id4321_UltrasonicSensor_0 (saved by Fritzing 0.7.4b)
breadboards: 1

parts:
  J1 = Infrared Proximity Sensor
  LED1 = LED - 5mm [color="Red (633nm)" package="5 mm [THT]"]
  LED2 = LED - 5mm [color="Red (633nm)" package="5 mm [THT]"]
  LED3 = LED - 5mm [color="Red (633nm)" package="5 mm [THT]"]
  LED4 = LED - 5mm [color="Red (633nm)" package="5 mm [THT]"]
  LED5 = LED - 5mm [color="Red (633nm)" package="5 mm [THT]"]
  LED6 = LED - 5mm [color="Red (633nm)" package="5 mm [THT]"]
  LED7 = LED - 5mm [color="Red (633nm)" package="5 mm [THT]"]
  LED8 = LED - 5mm [color="Red (633nm)" package="5 mm [THT]"]
  LED9 = LED - 5mm [color="Red (633nm)" package="5 mm [THT]"]
  LED10 = LED - 5mm [color="Red (633nm)" package="5 mm [THT]"]
  Arduino1 = Arduino

nets:
  N1: J1.Vout, Arduino1.D2
  GND: J1.GND, LED1.cathode, LED2.cathode, LED3.cathode, LED4.cathode, LED5.cathode, LED6.cathode, LED7.cathode, LED8.cathode, LED9.cathode, LED10.cathode, Arduino1.GND
  VCC: J1.Vcc, Arduino1.+5V
  N2: LED1.anode, Arduino1.D3
  N3: LED2.anode, Arduino1.D4
  N4: LED3.anode, Arduino1.D5
  N5: LED4.anode, Arduino1.D6
  N6: LED5.anode, Arduino1.D7
  N7: LED6.anode, Arduino1.D8
  N8: LED7.anode, Arduino1.D9
  N9: LED8.anode, Arduino1.D10
  N10: LED9.anode, Arduino1.D11
  N11: LED10.anode, Arduino1.D12
