# Fritzing sketch id4322_PING___LED_Display_0 (saved by Fritzing 0.9.2b)
breadboards: 1

parts:
  Part1 = Arduino Uno (Rev3)
  R6 = Resistor [tolerance=±5% resistance=560 package="2010 [SMD]"]
  R7 = Resistor [tolerance=±5% resistance=560 package="2010 [SMD]"]
  R8 = Resistor [tolerance=±5% resistance=560 package="2010 [SMD]"]
  R9 = Resistor [tolerance=±5% resistance=560 package="2010 [SMD]"]
  R10 = Resistor [tolerance=±5% resistance=560 package="2010 [SMD]"]
  R11 = Resistor [tolerance=±5% resistance=560 package="2010 [SMD]"]
  LED1 = LED - 5mm [color="Red (633nm)" package="5 mm [THT]"]
  LED2 = LED - 5mm [color="Red (633nm)" package="5 mm [THT]"]
  LED3 = LED - 5mm [color="Red (633nm)" package="5 mm [THT]"]
  LED4 = LED - 5mm [color="Red (633nm)" package="5 mm [THT]"]
  LED5 = LED - 5mm [color="Red (633nm)" package="5 mm [THT]"]
  LED6 = LED - 5mm [color="Red (633nm)" package="5 mm [THT]"]
  LED7 = LED - 5mm [color="Red (633nm)" package="5 mm [THT]"]
  LED8 = LED - 5mm [color="Red (633nm)" package="5 mm [THT]"]
  LED9 = LED - 5mm [color="Red (633nm)" package="5 mm [THT]"]
  LED10 = LED - 5mm [color="Red (633nm)" package="5 mm [THT]"]
  R12 = Resistor [tolerance=±5% resistance=560 package="2010 [SMD]"]
  R13 = Resistor [tolerance=±5% resistance=560 package="2010 [SMD]"]
  R14 = Resistor [tolerance=±5% resistance=560 package="2010 [SMD]"]
  R15 = Resistor [tolerance=±5% resistance=560 package="2010 [SMD]"]

nets:
  N1: Part1.D8, LED4.anode
  N2: Part1.D9_PWM, LED5.anode
  N3: Part1.D10_PWM/SS, LED6.anode
  N4: Part1.D11_PWM/MOSI, LED7.anode
  N5: Part1.D12/MISO, LED8.anode
  N6: Part1.D13/SCK, LED1.anode
  N7: Part1.GND, R6.Pin_1, R7.Pin_1, R8.Pin_1, R9.Pin_1, R10.Pin_1, R11.Pin_1, R12.Pin_1, R13.Pin_1, R14.Pin_1, R15.Pin_1
  N8: Part1.D4, LED9.anode
  N9: Part1.D5_PWM, LED10.anode
  N10: Part1.D6_PWM, LED2.anode
  N11: Part1.D7, LED3.anode
  N12: R6.Pin_0, LED8.cathode
  N13: R7.Pin_0, LED1.cathode
  N14: R8.Pin_0, LED6.cathode
  N15: R9.Pin_0, LED5.cathode
  N16: R10.Pin_0, LED7.cathode
  N17: R11.Pin_0, LED4.cathode
  N18: LED2.cathode, R13.Pin_0
  N19: LED3.cathode, R12.Pin_0
  N20: LED9.cathode, R15.Pin_0
  N21: LED10.cathode, R14.Pin_0

notes:
  This is designed for a 3 pin Ultrasonic Sensor PING))) Yellow is SIG, Red is VCC, Black is GND.
