# Fritzing sketch id4323_Ultrasonic_0 (saved by Fritzing 0.9.1b)
breadboards: 1

parts:
  Onderdeel1 = SRF05 Ultrasonic Rangefinder
  Onderdeel2 = Arduino Mega 2560 (Rev3)
  LED1 = LEDs [package=led10mm]
  R1 = Resistor [tolerance=±5% resistance=220 power=5W package=THT]

nets:
  N1: Onderdeel1.connector9, Onderdeel2.D3_PWM
  N2: Onderdeel1.connector10, Onderdeel2.D2_PWM
  N3: Onderdeel1.connector11, R1.Pin_0
  N4: Onderdeel2.D4_PWM, LED1.C
  N5: LED1.A, R1.Pin_1
