# Fritzing sketch id4324_ultrason_hcsr04_0 (saved by Fritzing 0.9.2b)
breadboards: 1

parts:
  Composant1 = Arduino Uno (Rev3)
  Composant2 = SRF05 Ultrasonic Rangefinder

nets:
  N1: Composant1.D11_PWM/MOSI, Composant2.connector10
  N2: Composant1.D12/MISO, Composant2.connector9
  N3: Composant1.5V, Composant2.connector8
  N4: Composant1.GND, Composant2.connector11
