# Fritzing sketch id4326_ultrasound_led_contral_0 (saved by Fritzing 0.9.3b)
breadboards: 1

parts:
  부품1 = Arduino Uno (Rev3)
  hc-sr1 = hc-sr04
  LED1 = LED - 5mm [color="Red (633nm)" package="5 mm [THT]"]
  R1 = Resistor [tolerance=±5% resistance=220 package=THT]

nets:
  GND: 부품1.GND, hc-sr1.GND, LED1.cathode
  N1: 부품1.D2, hc-sr1.Trig
  N2: 부품1.D3_PWM, hc-sr1.Echo
  N3: 부품1.D4, R1.Pin_1
  5V: 부품1.5V, hc-sr1.VCC
  N4: LED1.anode, R1.Pin_0
