# Fritzing sketch id4328_Umbraduino2_0 (saved by Fritzing 0.7.0b)
breadboards: 1

parts:
  Power_plug_-_9V+ = Power plug
  7805 = Voltage Regulator - 5V [package="TO220 [THT]"]
  D4_-_Rectifier_diode = Rectifier Diode [part_number=1N4001 package="300 mil [THT]"]
  J17 = female pin header, 4 pins [form="♀ (female)"]
  XTAL4 = Crystal [frequency="16 Mhz" package=THT]
  S6 = Pushbutton [package=THT]
  R1 = Resistor [tolerance=±5% resistance=1k package=THT]
  C12 = Electrolytic Capacitor [capacitance=10µF package="100 mil [THT, electrolytic]"]
  R2 = Resistor [tolerance=±5% resistance=220 package=THT]
  U7 = atmega168 [package="DIP28 [THT]"]
  C11 = Electrolytic Capacitor [capacitance=10µF package="100 mil [THT, electrolytic]"]
  C13 = Ceramic Capacitor [capacitance=100nF package="100 mil [THT, multilayer]"]
  C14 = Ceramic Capacitor [capacitance=100nF package="100 mil [THT, multilayer]"]
  ISP = Generic_male_header___3_pins [form="♂ (male)"]
  IPS2 = AVR_6_pin_ISP___First_3_pins [form="♂ (male)"]
  Signal_LED = LED - 5mm [color="Red (633nm)" package="5 mm [THT]"]
  R3 = Resistor [tolerance=±5% resistance=220 package=THT]
  C15 = Ceramic Capacitor [capacitance=22µF package="100 mil [THT, multilayer]"]
  PWR_LED = LED - 5mm [color="Red (633nm)" package="5 mm [THT]"]
  J19 = female pin header, 5 pins [form="♀ (female)"]
  J20 = female pin header, 6 pins [form="♀ (female)"]
  J18 = female pin header, 6 pins [form="♀ (female)"]

nets:
  GND: Power_plug_-_9V+.GND, 7805.GND, S6.leg1, C12.-, R2.Pin_0, U7.Pin_8, U7.Pin_22, C11.-, C13.1, C14.1, IPS2.connector2, R3.Pin_0, C15.1
  N1: Power_plug_-_9V+.VCC, D4_-_Rectifier_diode.anode
  N2: 7805.input_voltage, D4_-_Rectifier_diode.cathode, C11.+
  N3: 7805.output_voltage, S6.leg0, R1.Pin_0, R1.Pin_1, C12.+, U7.Pin_1, U7.Pin_7, U7.Pin_20, U7.Pin_21, ISP.connector2, IPS2.connector1, C15.0, PWR_LED.anode, J18.pin1
  N4: J17.pin1, U7.Pin_11
  N5: J17.pin2, U7.Pin_12
  N6: J17.pin3, U7.Pin_13
  N7: J17.pin4, U7.Pin_14
  N8: XTAL4.pin_0, U7.Pin_9, C13.0
  N9: XTAL4.pin_1, U7.Pin_10, C14.0
  N10: R2.Pin_1, PWR_LED.cathode
  N11: U7.Pin_2, J18.pin2
  N12: U7.Pin_3, J18.pin3
  N13: U7.Pin_4, J18.pin4
  N14: U7.Pin_5, J18.pin5
  N15: U7.Pin_6, J18.pin6
  N16: U7.Pin_15, J19.pin1
  N17: U7.Pin_16, J19.pin2
  N18: U7.Pin_17, IPS2.connector0, J19.pin3
  N19: U7.Pin_18, ISP.connector0, J19.pin4
  N20: U7.Pin_19, ISP.connector1, Signal_LED.anode, J19.pin5
  N21: U7.Pin_23, J20.pin1
  N22: U7.Pin_24, J20.pin2
  N23: U7.Pin_25, J20.pin3
  N24: U7.Pin_26, J20.pin4
  N25: U7.Pin_27, J20.pin5
  N26: U7.Pin_28, J20.pin6
  N27: Signal_LED.cathode, R3.Pin_1

notes:
  The Umbraduino
  This is essentially a breaboard Arduino with some differences:
  - no FTDI chip (so no serial bootloader burn magic)
  - 6-pin IDC to connect the AVRISP mkII (IDC1 + IDC2)
  - the signal LED will blink with the Arduino bootloader installed with the default blink sketch (test of successful install of bootloader)
  GND
  +5V Vcc
  Dimensions:
  - bore holes : 90.0mm x 45.0mm
  - board : 107.0mm x 57.0mm
  Distance from horiz. end / vert. end to center of bore holes (measured): 4.5mm / 4.5mm
  Hole diameter: 2.5mm
  Hole radius: 1.25mm
  Hole radius w./ring : 1.75
  Dist. from side to side of hole: 4.5mm - 1.75 = 2.75mm
  FTDI +5V bzw. +3,3V an Vcc Arduino FTDI Gnd mit Gnd Arduino FTDI RX mit TX Arduino FTDI TX mit RX Arduino FTDI DTR nit 100nF an Reset Arduino FTDI CTS wird nicht benötigt
  Ubrarduino, The Ubrarduino - an Arduino clone by OJ, 1.2
