# Fritzing sketch id432_walkLED_0 (saved by Fritzing 0.7.0b)
breadboards: 1

parts:
  Arduino1 = Arduino
  S1 = Pushbutton [package=THT]
  S2 = Pushbutton [package=THT]
  LED1 = LED - 5mm [color="Yellow (595nm)" package="5 mm [THT]"]
  LED2 = LED - 5mm [color="Red (633nm)" package="5 mm [THT]"]
  LED3 = LED - 5mm [color="Yellow (595nm)" package="5 mm [THT]"]
  LED4 = LED - 5mm [color="Red (633nm)" package="5 mm [THT]"]
  LED5 = LED - 5mm [color="Red (633nm)" package="5 mm [THT]"]
  LED6 = LED - 5mm [color="Yellow (595nm)" package="5 mm [THT]"]
  R1 = Rotary Potentiometer (Small) [maximum_resistance=100kΩ]
  R2 = Resistor [tolerance=±5% resistance=220 package=THT]
  R3 = Resistor [tolerance=±5% resistance=220 package=THT]
  R4 = Resistor [tolerance=±5% resistance=220 package=THT]
  R5 = Resistor [tolerance=±5% resistance=220 package=THT]
  R6 = Resistor [tolerance=±5% resistance=220 package=THT]
  R7 = Resistor [tolerance=±5% resistance=220 package=THT]
  R8 = Resistor [tolerance=±5% resistance=100 package=THT]
  R9 = Resistor [tolerance=±5% resistance=100 package=THT]

nets:
  N1: Arduino1.GND, LED1.cathode, LED2.cathode, LED3.cathode, LED4.cathode, LED5.cathode, LED6.cathode, R1.leg2, R8.Pin_1, R9.Pin_1
  N2: Arduino1.D12, R2.Pin_1
  N3: Arduino1.D11, R3.Pin_1
  N4: Arduino1.D10, R4.Pin_1
  N5: Arduino1.D9, R5.Pin_1
  N6: Arduino1.D8, R6.Pin_1
  N7: Arduino1.D7, R7.Pin_1
  N8: Arduino1.D4, S2.leg0, R8.Pin_0
  N9: Arduino1.D2, S1.leg0, R9.Pin_0
  N10: Arduino1.+5V, S1.leg1, S2.leg1, R1.leg1
  N11: Arduino1.A0, R1.wiper
  N12: LED1.anode, R3.Pin_0
  N13: LED2.anode, R4.Pin_0
  N14: LED3.anode, R5.Pin_0
  N15: LED4.anode, R2.Pin_0
  N16: LED5.anode, R6.Pin_0
  N17: LED6.anode, R7.Pin_0
