# Fritzing sketch id4332_unipolar_0 (saved by Fritzing 0.7.7b)
breadboards: 1

parts:
  Arduino1 = Arduino
  IC1 = ULN2003A [package="DIP16 [THT]"]
  M1 = Stepper Motor - Unipolar  # not connected

nets:
  N1: Arduino1.D11, IC1.In_4
  N2: Arduino1.D10, IC1.In_3
  N3: Arduino1.D9, IC1.In_2
  N4: Arduino1.D8, IC1.In_1
  N5: Arduino1.GND, IC1.0V

notes:
  Unipolar Stepper with ULN2003A
  [http://blog.ozzie.web.id/?p=1046]
