# Fritzing sketch id4333_ClimateSensor_0 (saved by Fritzing 0.9.2b)
breadboards: 1

parts:
  Bauteil1 = Arduino Uno (Rev3)
  DHT1 = DHT11_Temperature_and_Humitidy_Sensor
  R1 = Resistor [tolerance=±5% resistance=10k package=THT]
  U1 = ESP8266_module [part_number=ESP8266]
  R2 = Resistor [tolerance=±5% resistance=2.2k package=THT]
  R3 = Resistor [tolerance=±5% resistance=1k package=THT]
  R4 = Resistor [tolerance=±5% resistance=10k package=THT]

nets:
  N1: Bauteil1.D8, U1.connector7
  N2: Bauteil1.D9_PWM, R3.Pin_1
  N3: Bauteil1.GND, DHT1.connector4, U1.connector6, R2.Pin_0
  N4: Bauteil1.D2, DHT1.connector2, R1.Pin_1
  N5: Bauteil1.3V3, U1.connector1, R4.Pin_1
  N6: Bauteil1.5V, DHT1.connector1, R1.Pin_0
  N7: U1.connector0, R2.Pin_1, R3.Pin_0
  N8: U1.connector5, R4.Pin_0
