# Fritzing sketch id4333_spin_trans (saved by Fritzing 0.9.3b)
breadboards: 1

parts:
  Part1 = Arduino Uno (Rev3)
  D1 = Rectifier Diode [part_number=1N4001 package="300 mil [THT]"]  # not connected
  Q1 = Basic FET N-Channel [package="D2Pak [SMD]"]
  R1 = Resistor [tolerance=±5% resistance=10k package="1206 [SMD]"]
  M1 = DC Motor
  VCC1 = Battery block 9V
  D2 = Rectifier Diode [part_number=1N4001 package="Melf DO-213 AB [SMD]"]
  S1 = Momentary Switch [package=ksa_sealed_tac_switch]

nets:
  N1: Part1.D9_PWM, Q1.Gate
  N2: Part1.D2, R1.Pin_1, S1.3
  N3: Part1.5V, S1.1
  N4: Part1.GND, Q1.source, R1.Pin_0, M1.pin_2, VCC1.-, D2.cathode
  N5: Q1.drain, M1.pin_1
