# Fritzing sketch id4334_Sketch_0 (saved by Fritzing 0.9.0b)
circuit board: 7.29643cm x 7.72535cm
breadboards: 1

parts:
  Bluetooth = Adafruit_Bluefruit_EZ_LINK_v1.0
  부품1 = Arduino Uno (Rev3)
  GPS1 = Adafruit_Ultimate_GPS_Breakout
  NFC = prefix0000

nets:
  N1: Bluetooth.connector2, 부품1.GND, GPS1.connector7, NFC.connector38
  N2: Bluetooth.connector4, 부품1.5V, NFC.connector37
  N3: Bluetooth.connector5, 부품1.D1/TX
  N4: Bluetooth.connector6, 부품1.D0/RX
  N5: 부품1.A4/SDA, NFC.connector36
  N6: 부품1.A5/SCL, NFC.connector35
  N7: 부품1.D10_PWM/SS, GPS1.connector6
  N8: 부품1.D11_PWM/MOSI, GPS1.connector5
  N9: 부품1.3V3, GPS1.connector1
