# Fritzing sketch id4337_Stepper_USB_0 (saved by Fritzing 0.7.10b)
breadboards: 1

parts:
  Part1 = Arduino USB Host Shield
  Arduino1 = Arduino  # not connected
  Part2 = EasyDriver_v44
  M1 = Stepper Motor - Bipolar
  Power_plug1 = Power plug

nets:
  N1: Part1.D2, Part2.DIR
  N2: Part1.D3, Part2.STEP
  GND: Part1.GND, Part2.GND, Power_plug1.GND
  N3: Part2.V+, Power_plug1.VCC
  N4: Part2.OUT2A, M1.A
  N5: Part2.OUT2B, M1.C
  N6: Part2.OUT1A, M1.B
  N7: Part2.OUT1B, M1.D

notes:
  12 Volts
