# Fritzing sketch id4338_USB_ISP_Programmer_5V___v1.1_0 (saved by Fritzing 0.9.3b)
circuit board: 6.2cm x 3.15cm
breadboards: 1

parts:
  IC1 = MICROCONTROLLER [package=dil28-3]
  D2 = Zener Diode [part_number=1N4729A breakdown_voltage=3.6V package="300 mil [THT]"]
  C1 = Ceramic Capacitor [capacitance=4.7µF voltage=16V package="1206 [SMD, multilayer]"]
  C3 = Ceramic Capacitor [capacitance=100nF voltage=16V package="0805 [SMD, multilayer]"]
  C2 = Ceramic Capacitor [capacitance=100nF voltage=16V package="0805 [SMD, multilayer]"]
  R2 = Resistor [tolerance=±5% resistance=10k package="0805 [SMD]"]
  XTAL1 = Crystal [frequency="16 Mhz" package=THT]
  C4 = Ceramic Capacitor [capacitance=10pF voltage=16V package="0805 [SMD, multilayer]"]
  C5 = Ceramic Capacitor [capacitance=10pF voltage=16V package="0805 [SMD, multilayer]"]
  R7 = Resistor [tolerance=±5% resistance=68 package="0805 [SMD]"]
  R10 = Resistor [tolerance=±5% resistance=1M package="0805 [SMD]"]
  R8 = Resistor [tolerance=±5% resistance=68 package="0805 [SMD]"]
  R9 = Resistor [tolerance=±5% resistance=1.5k package="0805 [SMD]"]
  J2 = double row male pin header, 6 pins [form="♂ (male)"]
  R11 = Resistor [tolerance=±5% resistance=220 package="0805 [SMD]"]
  R12 = Resistor [tolerance=±5% resistance=220 package="0805 [SMD]"]
  D3 = Zener Diode [part_number=1N4729A breakdown_voltage=3.6V package="300 mil [THT]"]
  J3 = male pin header, 7 pins [form="♂ (male)"]
  LED2 = LED - 3mm [color="Red (633nm)" package="3 mm [THT]"]
  LED1 = LED - 3mm [color="Green (560nm)" package="3 mm [THT]"]
  J5 = male pin header, 2 pins [form="♂ (male)"]
  Pad2 = Pad [width=6.25 height=1.25 connect=center]
  Pad3 = Pad [width=1.25 height=1.25 connect=center]
  Pad4 = Pad [width=1.25 height=1.25 connect=center]
  C6 = Ceramic Capacitor [capacitance=100nF voltage=16V package="0805 [SMD, multilayer]"]
  J4 = male pin header, 3 pins [form="♂ (male)"]
  X1 = USB Connectors [package=usb-b-pth]
  Pad6 = Pad [width=2 height=1.5 connect=center]
  Pad5 = Pad [width=2 height=1.5 connect=center]

nets:
  N1: IC1.PC6(_RESET), R2.Pin_0, C6.1, J4.pin3
  N2: IC1.PD1(TXD), R8.Pin_0
  N3: IC1.PD2(INT0), R7.Pin_0
  5V: IC1.VCC, IC1.AVCC, C1.1, C2.1, R2.Pin_1, R9.Pin_0, R11.Pin_1, R12.Pin_1, J3.pin1, J5.pin2, X1.VBUS
  GND: IC1.GND, IC1.AGND, D2.anode, C1.0, C3.0, C2.0, C4.0, C5.0, R10.Pin_0, J2.pin1, D3.anode, J3.pin7, Pad2.pad, Pad3.pad, Pad4.pad, C6.0, X1.GND, Pad6.pad, Pad5.pad
  N4: IC1.PB6(XTAL1_TOSC1), XTAL1.pin_0, C4.1
  N5: IC1.PB7(XTAL2_TOSC2), XTAL1.pin_1, C5.1
  N6: IC1.PB0(ICP), J4.pin1
  N7: IC1.PB2(SS_OC1B), LED1.cathode
  MOSI: IC1.PB3(MOSI_OC2), J2.pin2
  MISO: IC1.PB4(MISO), J2.pin4
  SCK: IC1.PB5(SCK), J2.pin5
  N8: IC1.PC0(ADC0), LED2.cathode
  PC1: IC1.PC1(ADC1), J3.pin6
  PC2: IC1.PC2(ADC2), J3.pin5
  PC3: IC1.PC3(ADC3), J3.pin4
  PC4: IC1.PC4(ADC4_SDA), J3.pin3
  PC5: IC1.PC5(ADC5_SCL), J3.pin2
  USB_D+: D2.cathode, R7.Pin_1, R10.Pin_1, X1.D+
  N9: C3.1, J2.pin3, J5.pin1
  USB_D-: R8.Pin_1, R9.Pin_1, D3.cathode, X1.D-
  nRST: J2.pin6, J4.pin2
  N10: R11.Pin_0, LED1.anode
  N11: R12.Pin_0, LED2.anode

notes:
  Programmation interface
  USB-ISP programmer - 1.1
  12MHz
  USB interface
  GPIO (for futur use)
  USB programmer for AVR chips, 1.1
  J4:
  Pins 1-2 connected to programm external device
  Pins 2-3 connected to programm IC1
  J5:
  Close to power supply target device from USB +5V
  Open for target with their own power supply
