# Fritzing sketch id433_Arduino_7_Seg___Clock_0 (saved by Fritzing 0.9.3b)
breadboards: 2

parts:
  U1 = 74HC595 [package="DIP16 [THT]"]
  U3 = 74HC595 [package="DIP16 [THT]"]
  U4 = 74HC595 [package="DIP16 [THT]"]
  U5 = 74HC595 [package="DIP16 [THT]"]
  Part1 = Arduino Nano (Rev3.0)
  DI1 = 7-Segment LED Display [package=THT]
  DI2 = 7-Segment LED Display [package=THT]
  DI3 = 7-Segment LED Display [package=THT]
  DI4 = 7-Segment LED Display [package=THT]
  R2 = Resistor [tolerance=±5% resistance=100 package=THT]
  R3 = Resistor [tolerance=±5% resistance=100 package=THT]
  R4 = Resistor [tolerance=±5% resistance=100 package=THT]
  R5 = Resistor [tolerance=±5% resistance=100 package=THT]

nets:
  N1: U1.Q1, DI1.cathodeG
  N2: U1.Q2, DI1.cathodeF
  N3: U1.Q3, DI1.cathodeE
  N4: U1.Q4, DI1.cathodeD
  N5: U1.Q5, DI1.cathodeC
  N6: U1.Q6, DI1.cathodeB
  N7: U1.Q7, DI1.cathodeA
  GND: U1.GND, U1.OE, U3.GND, U3.OE, U4.GND, U4.OE, U5.GND, U5.OE, Part1.GND, Part1.D3
  VCC: U1.MR, U1.VCC, U3.MR, U3.VCC, U4.MR, U5.MR, U5.VCC, Part1.5V
  N8: U1.ST_CP, Part1.D13/SCK
  N9: U1.DS, Part1.D2
  N10: U3.Q1, DI4.cathodeG
  N11: U3.Q2, DI4.cathodeF
  N12: U3.Q3, DI4.cathodeE
  N13: U3.Q4, DI4.cathodeD
  N14: U3.Q5, DI4.cathodeC
  N15: U3.Q6, DI4.cathodeB
  N16: U3.Q7, DI4.cathodeA
  N17: U3.SH_CP, Part1.D7
  N18: U3.ST_CP, Part1.D9
  N19: U3.DS, Part1.D8
  N20: U4.Q1, DI3.cathodeG
  N21: U4.Q2, DI3.cathodeF
  N22: U4.Q3, DI3.cathodeE
  N23: U4.Q4, DI3.cathodeD
  N24: U4.Q5, DI3.cathodeC
  N25: U4.Q6, DI3.cathodeB
  N26: U4.Q7, DI3.cathodeA
  N27: U4.SH_CP, Part1.D4
  N28: U4.ST_CP, Part1.D6
  N29: U4.DS, Part1.D5
  N30: U5.Q1, DI2.cathodeG
  N31: U5.Q2, DI2.cathodeF
  N32: U5.Q3, DI2.cathodeE
  N33: U5.Q4, DI2.cathodeD
  N34: U5.Q5, DI2.cathodeC
  N35: U5.Q6, DI2.cathodeB
  N36: U5.Q7, DI2.cathodeA
  N37: U5.SH_CP, Part1.D10
  N38: U5.ST_CP, Part1.D12/MISO
  N39: U5.DS, Part1.D11/MOSI
  N40: DI1.commAnode#2, R5.Pin_1
  N41: DI2.commAnode#2, R2.Pin_1
  N42: DI3.commAnode#2, R4.Pin_1
  N43: DI4.commAnode#2, R3.Pin_1
  N44: R2.Pin_0, R3.Pin_0, R4.Pin_0, R5.Pin_0
