# Fritzing sketch id4340_USB_plug_0 (saved by Fritzing 0.8.7b)
circuit board: 3.00284cm x 1.21732cm
breadboards: 1

parts:
  part = USB Connectors [package=usb-a-pcb]
  part_2 = female pin header, 2 pins [form="♀ (female)"]
  part_3 = female pin header, 2 pins [form="♀ (female)"]

nets:
  N1: part.VBUS, part_3.pin2
  N2: part.GND, part_2.pin1
  N3: part.D-, part_3.pin1
  N4: part.D+, part_2.pin2

notes:
  www.cypherdeck.org
  USB
  red
  white
  green
  black
