# Fritzing sketch id4341_OPEN_DMX_adapter_0 (saved by Fritzing 0.7.10b)
breadboards: 1

parts:
  IC1 = IC, DIP package, 8 pins [chip_label=IC spacing=300mil]
  R1 = Resistor [resistance=100 tolerance=±5% package=THT]
  J1 = screw terminal, 3 pins

nets:
  N1: IC1.pin1, R1.Pin_0
  N2: IC1.pin2, IC1.pin5, R1.Pin_1, J1.pin3
  N3: IC1.pin3, IC1.pin8
  N4: IC1.pin6, J1.pin1
  N5: IC1.pin7, J1.pin2

notes:
  MAX485CPA
  RS-422/RS-485 Interface IC
  100ohm Resistor
  DMX OUT (+) (-) (GND)
  Blau an RS232 pin 3 TxD
  Schwarz an RS232 pin 5 Gnd
  Rot an RS 232 pin 2 RxD
  an USB to RS232 with FTDI chip
