# Fritzing sketch id4342_Reference_Design_0 (saved by Fritzing 0.9.2b)
breadboards: 1

parts:
  USB_TO_HDMI_MODULE2 = prefix1110
  USB_TYPE_C1 = prefix1020
  Analog_Switchs1 = prefix1003 [part_number=MAX4659]
  USB_TYPE_C2 = prefix1001
  LM1 = prefix2001
  R1 = Resistor [tolerance=±5% resistance=220 package="2512 [SMD]"]
  R2 = Resistor [tolerance=±5% resistance=220 package="2512 [SMD]"]
  D1 = Rectifier Diode [part_number=1N4001 package="300 mil [THT]"]
  R3 = Resistor [tolerance=±5% resistance=220 package="2512 [SMD]"]
  元件1 = prefix3000
  USB_3_0_Micro_B_Female1 = prefix4000 [part_number="USB 3.0 Micro B Female"]

nets:
  N1: USB_TO_HDMI_MODULE2.connector0, 元件1.connector17, USB_3_0_Micro_B_Female1.connector0
  N2: USB_TO_HDMI_MODULE2.connector1, 元件1.connector59
  N3: USB_TO_HDMI_MODULE2.connector2, 元件1.connector58
  N4: USB_TO_HDMI_MODULE2.connector3, USB_TO_HDMI_MODULE2.connector8, 元件1.connector39, USB_3_0_Micro_B_Female1.connector6
  N5: USB_TO_HDMI_MODULE2.connector4, 元件1.connector50
  N6: USB_TO_HDMI_MODULE2.connector5, 元件1.connector49
  N7: USB_TO_HDMI_MODULE2.connector6, 元件1.connector46
  N8: USB_TO_HDMI_MODULE2.connector7, 元件1.connector47
  N9: USB_TYPE_C1.connector0, USB_TYPE_C1.connector12
  N10: USB_TYPE_C1.connector3, USB_TYPE_C1.connector9, USB_TYPE_C1.connector16, USB_TYPE_C1.connector21, USB_TYPE_C2.connector3, USB_TYPE_C2.connector9, USB_TYPE_C2.connector16, USB_TYPE_C2.connector21, LM1.connector3, LM1.connector4, D1.anode
  N11: USB_TYPE_C1.connector5, USB_TYPE_C1.connector18, 元件1.connector56
  N12: USB_TYPE_C1.connector6, USB_TYPE_C1.connector19, 元件1.connector57
  N13: USB_TYPE_C1.connector7, Analog_Switchs1.connector0
  N14: USB_TYPE_C1.connector10, 元件1.connector6
  N15: USB_TYPE_C1.connector11, 元件1.connector5
  N16: USB_TYPE_C1.connector13, USB_TYPE_C1.connector24
  N17: USB_TYPE_C1.connector17, USB_TYPE_C2.connector17
  N18: USB_TYPE_C1.connector22, 元件1.connector7
  N19: USB_TYPE_C1.connector23, 元件1.connector8
  N20: Analog_Switchs1.connector1, R3.Pin_0
  N21: Analog_Switchs1.connector2, R3.Pin_1
  N22: Analog_Switchs1.connector7, USB_TYPE_C2.connector7
  N23: USB_TYPE_C2.connector0, USB_TYPE_C2.connector12
  N24: USB_TYPE_C2.connector13, USB_TYPE_C2.connector24
  N25: LM1.connector0, D1.cathode
  N26: LM1.connector2, R1.Pin_1, R2.Pin_1
  N27: LM1.connector5, R1.Pin_0, 元件1.connector16
  N28: 元件1.connector40, USB_3_0_Micro_B_Female1.connector11
  N29: 元件1.connector41, USB_3_0_Micro_B_Female1.connector10
  N30: 元件1.connector43, USB_3_0_Micro_B_Female1.connector7
  N31: 元件1.connector44, USB_3_0_Micro_B_Female1.connector8
  N32: 元件1.connector61, USB_3_0_Micro_B_Female1.connector2
  N33: 元件1.connector62, USB_3_0_Micro_B_Female1.connector4

notes:
  GND
  5.1k ohm
  SYS PWR +5V
  USB TYPE C PLUG-IN DETECT
  [USB TYPE C POWER ADAPTOR]
  [20v~5V Vin 5V Vout, Step Down Regulator]
  U3 HUB
  USB 3.0 Receptacle
  HDMI 1.3a Output
