# Fritzing sketch id4343_USBPower1.01r_0 (saved by Fritzing 0.9.2b)
circuit board: 9.23252cm x 3.03561cm
breadboards: 1

parts:
  Conn_7 = USB connector [package=THT]
  Conn_8 = USB connector [package=THT]
  Conn_9 = USB connector [package=THT]
  Conn_10 = USB connector [package=THT]
  Conn_11 = USB connector [package=THT]
  Conn_12 = USB connector [package=THT]
  R1_-_D+ = Resistor [tolerance=±5% resistance=220 package=THT]
  R2_-_D+ = Resistor [tolerance=±5% resistance=220 package=THT]
  R1_-_D- = Resistor [tolerance=±5% resistance=220 package=THT]
  R2_-_D- = Resistor [tolerance=±5% resistance=220 package=THT]
  +5v = Pad [width=5 height=6 connect=center]
  0v = Pad [width=5 height=6 connect=center]  # not connected

nets:
  5V: Conn_7.5V, Conn_8.5V, Conn_9.5V, Conn_10.5V, Conn_11.5V, Conn_12.5V, R1_-_D+.Pin_0, R1_-_D-.Pin_0, +5v.pad
  N1: Conn_7.d-, Conn_8.d-, Conn_9.d-, Conn_10.d-, Conn_11.d-, Conn_12.d-, R1_-_D-.Pin_1, R2_-_D-.Pin_0
  N2: Conn_7.d+, Conn_8.d+, Conn_9.d+, Conn_10.d+, Conn_11.d+, Conn_12.d+, R1_-_D+.Pin_1, R2_-_D+.Pin_0
  GND: Conn_7.GND, Conn_7.chassis5, Conn_8.GND, Conn_8.chassis5, Conn_8.chassis6, Conn_9.GND, Conn_9.chassis5, Conn_9.chassis6, Conn_10.GND, Conn_10.chassis5, Conn_10.chassis6, Conn_11.GND, Conn_11.chassis5, Conn_11.chassis6, Conn_12.GND, Conn_12.chassis5, Conn_12.chassis6, R2_-_D+.Pin_1, R2_-_D-.Pin_1
