# Fritzing sketch id4344_push_btn_25_0 (saved by Fritzing 0.7.12b)
breadboards: 1

parts:
  S1 = Pushbutton [package="[THT]"]
  R1 = Resistor [tolerance=±5% resistance=10k package=THT]
  R2 = Resistor [tolerance=±5% resistance=1k package=THT]
  Raspberry_Pi1 = Raspberry_Pi__Model_B

nets:
  N1: S1.Pin_3, R2.Pin_1
  N2: R1.Pin_0, Raspberry_Pi1.connector1
  N3: R2.Pin_0, Raspberry_Pi1.connector22

notes:
  USE GPIO 25 (BCM Numbering) as input
