# Fritzing sketch id4345_Useless_Box_0 (saved by Fritzing 0.9.2b)

parts:
  부품1 = Arduino Uno (Rev3)
  S1 = Toggle Switch [package=THT]
  J1 = Basic Servo

nets:
  N1: 부품1.D9_PWM, J1.pulse
  N2: 부품1.D13/SCK, S1.L1
  GND: 부품1.GND, S1.COM, J1.gnd
  5V: 부품1.5V, J1.vcc
