# Fritzing sketch id4347_LED_LOW_BATTERY_INDICATOR_0 (saved by Fritzing 0.7.1b)
stripboards: 1

parts:
  R1 = Resistor [tolerance=±5% resistance=10k package=THT]
  R3 = Resistor [tolerance=±5% resistance=10k package=THT]
  T1 = Trimmer Potentiometer [maximum_resistance=10kΩ package=THT]
  R2 = Resistor [tolerance=±5% resistance=10k package=THT]
  R5 = Resistor [tolerance=±5% resistance=10k package=THT]
  R4 = Resistor [tolerance=±5% resistance=1k package=THT]
  R6 = Resistor [tolerance=±5% resistance=1k package=THT]
  LED1 = LED - 3mm [color="Green (565nm)" package="3 mm [THT]"]
  Q4 = NPN-Transistor [package="TO92 [THT]"]
  Q1 = NPN-Transistor [package="TO92 [THT]"]
  Q2 = NPN-Transistor [package="TO92 [THT]"]
  Q5 = NPN-Transistor [package="TO92 [THT]"]
  VCC1 = Battery
  LED2 = LED - 3mm [color="Red (633nm)" package="3 mm [THT]"]
  Q3 = NPN-Transistor [package="TO92 [THT]"]

nets:
  N1: R1.Pin_0, T1.wiper
  N2: R1.Pin_1, Q1.B
  N3: R3.Pin_0, R3.Pin_1, T1.leg1, T1.leg2, R2.Pin_0, R2.Pin_1, R5.Pin_0, R5.Pin_1, R4.Pin_0, R4.Pin_1, R6.Pin_0, R6.Pin_1, LED1.cathode, LED1.anode, Q4.E, Q4.B, Q4.C, Q1.E, Q1.C, Q2.E, Q2.B, Q2.C, Q5.E, Q5.B, Q5.C, VCC1.-, VCC1.+, LED2.cathode, LED2.anode, Q3.E, Q3.B, Q3.C
