# Fritzing sketch id4348_UserBot_Schematic_0 (saved by Fritzing 0.9.2b)
circuit board: 6.88566cm x 5.36311cm
breadboards: 1

parts:
  Arduino1 = Arduino Uno (Rev3)
  R1 = Resistor [tolerance=±5% resistance=330 package=THT]
  C1 = Electrolytic Capacitor [capacitance=10µF package="100 mil [THT, electrolytic]"]
  NRF24L1 = NRF24L01
  S1 = Pushbutton [package="[THT]"]
  R2 = Resistor [tolerance=±5% resistance=10k package=THT]

nets:
  N1: Arduino1.A0, S1.Pin_3, S1.Pin_4, R2.Pin_1
  N2: Arduino1.D9_PWM, NRF24L1.connector5
  N3: Arduino1.D10_PWM/SS, NRF24L1.connector1
  N4: Arduino1.D11_PWM/MOSI, NRF24L1.connector2
  N5: Arduino1.D12/MISO, NRF24L1.connector7
  N6: Arduino1.D13/SCK, NRF24L1.connector6
  GND: Arduino1.GND, R1.Pin_0, C1.-, NRF24L1.connector4, S1.Pin_1, S1.Pin_2
  N7: Arduino1.D3_PWM, R1.Pin_1
  3.3V: Arduino1.3V3, C1.+, NRF24L1.connector0
  5V: Arduino1.5V, R2.Pin_0

notes:
  Basic Configuration for a Open Grow GroBot (User Bot)
  The communications between your Arduino and the GroNode is made via the NRF24L01 Module.
  The source firmware is designed to handle one button and one led.
  UserBot
