# Fritzing sketch id434_LCD_Arduino_FreeNAS (saved by Fritzing 0.4.3b)
breadboards: 1

parts:
  Arduino1 = Arduino
  R2 = Resistor [resistance=12 package=THT]
  LCD1 = LCD screen
  R1 = Trimmer Potentiometer [package=THT]

nets:
  N1: Arduino1.D7, LCD1.RS
  N2: Arduino1.D6, LCD1.E
  N3: Arduino1.D5, LCD1.DB4
  N4: Arduino1.D4, LCD1.DB5
  N5: Arduino1.D3, LCD1.DB6
  N6: Arduino1.D2, LCD1.DB7
  +5V: Arduino1.+5V, R2.Pin_0, LCD1.VDD, R1.leg2
  GND: Arduino1.GND, LCD1.VSS, LCD1.R/W, LCD1.LED-, R1.leg1
  N7: R2.Pin_1, LCD1.LED+
  N8: LCD1.V0, R1.wiper

notes:
  Proyecto Arduino-FreeNAS
  Conexión Arduino-LCD
  Prototipo: P01LCD v1.0
