# Fritzing sketch id4350_MATLAB_with_Bluetooth_0 (saved by Fritzing 0.9.3b)
breadboards: 1

parts:
  Part1 = Arduino Uno (Rev3) - ICSP
  Part2 = Bluetooth HC-05 Macho  # not connected
  LED1 = LED - 3mm [color="Red (633nm)" package="3 mm [THT]"]

nets:
  N1: Part1.ICSP_MOSI, Part1.D11_PWM/MOSI, LED1.anode
