# Fritzing sketch id4351_HC_SR04_0 (saved by Fritzing 0.9.3b)
breadboards: 1

parts:
  Raspberry_Pi_3 = Raspberry Pi 3
  HC-SR04 = hc-sr04
  R1 = Resistor [tolerance=±5% resistance=2k package=THT]
  R2 = Resistor [tolerance=±5% resistance=2k package=THT]

nets:
  N1: Raspberry_Pi_3.GPIO24, R1.Pin_1, R2.Pin_0
  N2: Raspberry_Pi_3.GPIO23, HC-SR04.Trig
  GND: Raspberry_Pi_3.GND, HC-SR04.GND
  5V: Raspberry_Pi_3.5V, HC-SR04.VCC, R2.Pin_1
  N3: HC-SR04.Echo, R1.Pin_0
