# Fritzing sketch id4352_Untitled_Sketch_4_0 (saved by Fritzing 0.9.0b)
breadboards: 1

parts:
  Part1 = Arduino Leonardo (Rev3b)
  IR1 = TSOP312.., 314.. [package=THT]
  LED1 = LED - 5mm [color="Red (633nm)" package="5 mm [THT]"]
  LED2 = LED - 5mm [color="Red (633nm)" package="5 mm [THT]"]
  LED3 = LED - 5mm [color="Red (633nm)" package="5 mm [THT]"]
  LED4 = LED - 5mm [color="Red (633nm)" package="5 mm [THT]"]
  LED5 = LED - 5mm [color="Red (633nm)" package="5 mm [THT]"]
  R1 = Resistor [tolerance=±5% resistance=220 package=THT]
  R2 = Resistor [tolerance=±5% resistance=220 package=THT]
  R3 = Resistor [tolerance=±5% resistance=220 package=THT]
  R4 = Resistor [tolerance=±5% resistance=220 package=THT]
  R5 = Resistor [tolerance=±5% resistance=220 package=THT]

nets:
  N1: Part1.D2/SDA, LED5.anode
  N2: Part1.D3_PWM/SCL, LED4.anode
  N3: Part1.D4/A6, LED3.anode
  N4: Part1.D5_PWM, LED2.anode
  N5: Part1.D6_PWM/A7, LED1.anode
  N6: Part1.5V, IR1.Data
  GND: Part1.GND, IR1.GND, R1.Pin_1, R2.Pin_1, R3.Pin_1, R4.Pin_1, R5.Pin_1
  N7: Part1.D11_PWM, IR1.Vs
  N8: LED1.cathode, R1.Pin_0
  N9: LED2.cathode, R2.Pin_0
  N10: LED3.cathode, R3.Pin_0
  N11: LED4.cathode, R4.Pin_0
  N12: LED5.cathode, R5.Pin_0
