# Fritzing sketch id4353_ButtonsToVarRGB_0 (saved by Fritzing 0.9.2b)
breadboards: 1

parts:
  Part1 = Arduino Uno (Rev3) - ICSP
  S1 = Pushbutton [package="[THT]"]
  S2 = Pushbutton [package="[THT]"]
  S3 = Pushbutton [package="[THT]"]
  R1 = Resistor [tolerance=±5% resistance=10k package=THT]
  R2 = Resistor [tolerance=±5% resistance=10k package=THT]
  R3 = Resistor [tolerance=±5% resistance=10k package=THT]
  LED1 = RGB LED (com. cathode, rgb) [package="5 mm [THT]"]

nets:
  N1: Part1.ICSP_MISO, Part1.D12/MISO, S1.Pin_3, S1.Pin_4, R1.Pin_0
  N2: Part1.ICSP_MOSI, Part1.D11_PWM/MOSI, S2.Pin_3, S2.Pin_4, R2.Pin_0
  N3: Part1.D10_PWM/SS, S3.Pin_3, S3.Pin_4, R3.Pin_0
  N4: Part1.GND, R1.Pin_1, R2.Pin_1, R3.Pin_1, LED1.common_cathode
  N5: Part1.D2, LED1.blue_anode
  N6: Part1.D3_PWM, LED1.green_anode
  N7: Part1.D4, LED1.red_anode
  N8: Part1.3V3, S1.Pin_1, S1.Pin_2, S2.Pin_1, S2.Pin_2, S3.Pin_1, S3.Pin_2

notes:
  On_Status1
  Off_Status1
  Mode
