# Fritzing sketch id4355_E5_Bluetooth_0 (saved by Fritzing 0.9.2b)
breadboards: 1

parts:
  HC-05 = Bluetooth HC-05 Macho
  Parte2 = Arduino Uno (Rev3)
  R1 = Resistor [tolerance=±5% resistance=470 package=THT]
  LED1 = LED - 5mm [color="Blue (430nm)" package="5 mm [THT]"]
  R2 = Resistor [tolerance=±5% resistance=10k package=THT]
  S1 = Pushbutton [package="[THT]"]
  R3 = Rotary Potentiometer (Small) [maximum_resistance=100kΩ package=THT]
  R4 = Resistor [tolerance=±5% resistance=470 package=THT]
  LED2 = LED - 5mm [color="Red (660nm)" package="5 mm [THT]"]
  R5 = Resistor [tolerance=±5% resistance=100 package=THT]
  R6 = Resistor [tolerance=±5% resistance=100 package=THT]
  R7 = Resistor [tolerance=±5% resistance=220 package=THT]
  LED3 = RGB LED (com. cathode, rgb) [package="5 mm [THT]"]

nets:
  N1: HC-05.State, R1.Pin_1
  N2: HC-05.TXD, Parte2.D10_PWM/SS
  N3: HC-05.RXD, Parte2.D11_PWM/MOSI
  N4: HC-05.VCC, Parte2.D8
  N5: HC-05.Key, Parte2.D9_PWM
  GND: HC-05.GND, Parte2.GND, LED1.cathode, R2.Pin_1, R3.leg1, LED2.cathode, LED3.common_cathode
  N6: Parte2.A0, R3.wiper
  N7: Parte2.D2, R2.Pin_0, S1.Pin_1, S1.Pin_2
  N8: Parte2.D3_PWM, R7.Pin_0
  N9: Parte2.D5_PWM, R6.Pin_0
  N10: Parte2.D6_PWM, R5.Pin_0
  N11: Parte2.D7, R4.Pin_1
  N12: Parte2.5V, S1.Pin_3, S1.Pin_4, R3.leg2
  N13: R1.Pin_0, LED1.anode
  N14: R4.Pin_0, LED2.anode
  N15: R5.Pin_1, LED3.blue_anode
  N16: R6.Pin_1, LED3.green_anode
  N17: R7.Pin_1, LED3.red_anode

notes:
  RX y TX indican donde conectarlo, estan invertidos con respecto a los pines.
