# Fritzing sketch id4356_WTV020_music_for_dog_0 (saved by Fritzing 0.9.2b)
breadboards: 1

parts:
  Componente1 = Arduino Uno (Rev3) - ICSP
  J1 = Basic Servo
  PIR2 = PIR_sensor
  IC1 = IC, DIP package, 16 pins [chip_label=IC]
  SP1 = SPEAKER [package=pcb_mount_speaker]
  Q1 = TRANSISTOR_NPN [package=to-92]
  Q2 = TRANSISTOR_NPN [package=to-92]
  R1 = Resistor [tolerance=±5% resistance=220 package="2010 [SMD]"]  # not connected
  R2 = Resistor [tolerance=±5% resistance=220 package="2010 [SMD]"]

nets:
  N1: Componente1.D13/SCK, R2.Pin_1
  N2: Componente1.D2, J1.pulse
  N3: Componente1.D3_PWM, PIR2.connector2
  N4: Componente1.3V3, PIR2.connector1, IC1.pin16
  N5: Componente1.GND, PIR2.connector3, IC1.pin8, Q1.C, Q2.C
  N6: IC1.pin4, SP1.-
  N7: IC1.pin5, SP1.+
  N8: IC1.pin9, Q1.E
  N9: IC1.pin13, Q2.E
  N10: Q2.B, R2.Pin_0

notes:
  1 pin
  16 pin
  Play
  Next
  wtv020
  By A.Oss 2016
