# Fritzing sketch id4357_Adafruit_18b20_matrice_0 (saved by Fritzing 0.9.2b)
breadboards: 1

parts:
  LED1 = 8x8_LED_Matrix__yellow
  Componente1 = Arduino Uno (Rev3)
  DS1 = DS18B20_1_Wire_Temperature_Sensor [part_number=DS18B20]
  R1 = Resistor [tolerance=±5% resistance=4.7k package=THT]

nets (from the schematic view):
  N1: LED1.connector1, Componente1.5V, DS1.connector1, R1.Pin_0
  N2: LED1.connector2, Componente1.GND, DS1.connector3
  N3: LED1.connector3, Componente1.A5/SCL
  N4: LED1.connector4, Componente1.A4/SDA
  N5: Componente1.D2, DS1.connector2, R1.Pin_1

notes:
  MATRICE...............ARDUINO
  Pin "C" .................... Pin A5
  Pin "D" .................... Pin A4
