# Fritzing sketch id4359_Untitled_Sketch_0 (saved by Fritzing 0.9.3b)
breadboards: 1

parts:
  Parça1 = Arduino Uno (Rev3)
  hc-sr1 = hc-sr04
  LED1 = LED - 5mm [color="Red (633nm)" package="5 mm [THT]"]
  LED2 = smd LED [color="Red (633nm)" package="0603 [SMD]"]
  LED3 = smd LED [color="Red (633nm)" package="0603 [SMD]"]
  LED4 = smd LED [color="Red (633nm)" package="0603 [SMD]"]
  R1 = Resistor [tolerance=±5% resistance=220 package=THT]
  R2 = Resistor [tolerance=±5% resistance=220 package=THT]
  R3 = Resistor [tolerance=±5% resistance=220 package=THT]
  R4 = Resistor [tolerance=±5% resistance=220 package=THT]
  J1 = Piezo Speaker

nets:
  N1: Parça1.D8, J1.pin2
  N2: Parça1.D2, R2.Pin_0
  N3: Parça1.D3_PWM, R3.Pin_0
  N4: Parça1.D4, R4.Pin_0
  N5: Parça1.D5_PWM, R1.Pin_0
  N6: Parça1.D7, hc-sr1.Trig
  5V: Parça1.5V, hc-sr1.VCC
  GND: Parça1.GND, hc-sr1.GND, LED1.cathode, LED2.cathode, LED3.cathode, LED4.cathode, J1.pin1
  N7: LED1.anode, R1.Pin_1
  N8: LED2.anode, R4.Pin_1
  N9: LED3.anode, R3.Pin_1
  N10: LED4.anode, R2.Pin_1
