# Fritzing sketch id4362_v4LAB___Big_Project_(Ultrasonic_Sensor_LCD)_0 (saved by Fritzing 0.9.3b)
breadboards: 1

parts:
  Part1 = Arduino Uno (Rev3)
  LCD1 = LCD screen
  S1 = Pushbutton [package="[THT]"]
  R1 = Resistor [tolerance=±5% resistance=220 package=THT]
  R2 = Rotary Potentiometer (Small) [maximum_resistance=100kΩ package=THT]
  Part2 = SRF05 Ultrasonic Rangefinder

nets:
  N1: Part1.D8, S1.Pin_1, S1.Pin_2, R1.Pin_1
  N2: Part1.D10_PWM/SS, LCD1.DB4
  N3: Part1.D11_PWM/MOSI, LCD1.DB5
  N4: Part1.D12/MISO, LCD1.DB6
  N5: Part1.D13/SCK, LCD1.DB7
  N6: Part1.D2, Part2.connector10
  N7: Part1.D3_PWM, Part2.connector9
  N8: Part1.D4, LCD1.R/W
  N9: Part1.D6_PWM, LCD1.DB0
  N10: Part1.3V3, LCD1.LED+
  5V: Part1.5V, LCD1.VDD, S1.Pin_3, S1.Pin_4, R2.leg1, Part2.connector8
  GND: Part1.GND, LCD1.VSS, LCD1.E, LCD1.LED-, R1.Pin_0, R2.leg2, Part2.connector11
  N11: LCD1.V0, R2.wiper
