# Fritzing sketch id4363_Voltage_Control_via_Potentiometer_&_Vactrol_0 (saved by Fritzing 0.9.3b)
breadboards: 1

parts:
  10kΩ = Photocell (LDR) [package=THT]
  Invert_VC_values = SWITCH_SPDT [package=kps-1290]
  LED1 = LEDs [package=fkit-led-1206]
  U3 = 2.5mm Audio Jack [package=stereojack2.5mm_stereojack2.5mm]
  Oscillator_control = Slide Potentiometer [maximum_resistance=10kΩ]
  R1 = Resistor [tolerance=±5% resistance=10 package=THT]

nets:
  GND: 10kΩ.pin_0, Invert_VC_values.S, U3.RIGHT, Oscillator_control.wiper, Oscillator_control.leg2
  N1: 10kΩ.pin_1, Invert_VC_values.P
  5V: Invert_VC_values.O, Oscillator_control.leg1
  N2: LED1.A, R1.Pin_1
  N3: LED1.C, U3.SLEEVE
  N4: U3.LEFT, R1.Pin_0
