# Fritzing sketch id4365_valgfag_2.1_0 (saved by Fritzing 0.9.3b)
circuit board: 8.46667cm x 5.64444cm
breadboards: 1

parts:
  MICROSWITCH_5A_M_RULLE = Toggle Switch [package=THT]
  microcontroller_Arduino_UNO = Arduino Nano (Rev3.0)
  2_color_LED_modul = DUO LED RG [package="5 mm [THT]"]
  R1 = Resistor [tolerance=±5% resistance=220 package=THT]
  pushbutton = Pushbutton [package="[THT]"]
  R2 = Resistor [tolerance=±5% resistance=220 package=THT]
  reset_LED = LED - 5mm [color="Green (570nm)" package="5 mm [THT]"]

nets:
  N1: MICROSWITCH_5A_M_RULLE.L1, MICROSWITCH_5A_M_RULLE.L2, microcontroller_Arduino_UNO.D2, R1.Pin_0
  N2: MICROSWITCH_5A_M_RULLE.COM, microcontroller_Arduino_UNO.5V
  N3: microcontroller_Arduino_UNO.RESET, pushbutton.Pin_1, pushbutton.Pin_2
  N4: microcontroller_Arduino_UNO.GND, R1.Pin_1, pushbutton.Pin_3, pushbutton.Pin_4, reset_LED.cathode
  N5: microcontroller_Arduino_UNO.D4, 2_color_LED_modul.red_anode
  N6: microcontroller_Arduino_UNO.D6, 2_color_LED_modul.green_anode
  N7: microcontroller_Arduino_UNO.D8, R2.Pin_0
  N8: R2.Pin_1, reset_LED.anode
