# Fritzing sketch id4366_Tabletop_fan_fritz_0 (saved by Fritzing 0.9.1b)
breadboards: 1

parts:
  Part1 = Arduino Uno (Rev3)
  R1 = Resistor [tolerance=±5% resistance=220 package=THT]
  LED1 = LED - 5mm [color="Red (633nm)" package="5 mm [THT]"]
  M1 = DC Motor
  Q1 = NPN-Transistor [package="TO92 [THT]"]
  VCC1 = Battery  # not connected
  R2 = Trimmer Potentiometer [maximum_resistance=10kΩ package=THT]
  R3 = Trimmer Potentiometer [maximum_resistance=10kΩ package=THT]

nets:
  N1: Part1.A0, R2.wiper
  N2: Part1.A2, R3.wiper
  N3: Part1.D9_PWM, Q1.E
  N4: Part1.D10_PWM/SS, R1.Pin_1
  N5: Part1.5V, Q1.B, R2.leg2, R3.leg2
  N6: Part1.GND, LED1.cathode, M1.pin_1, R2.leg1, R3.leg1
  N7: R1.Pin_0, LED1.anode
  N8: M1.pin_2, Q1.C
