# Fritzing sketch id4367_zumbador_potenciometro_0 (saved by Fritzing 0.9.3b)

parts:
  Componente1 = Arduino Uno (Rev3)
  R1 = Rotary Potentiometer (Small) [maximum_resistance=100kΩ package=THT]
  J1 = Piezo Speaker

nets:
  N1: Componente1.A0, R1.wiper
  N2: Componente1.GND, R1.leg1, J1.pin1
  N3: Componente1.D3_PWM, J1.pin2
  N4: Componente1.5V, R1.leg2

notes:
  Zumbador > PIN DIGITAL 3
  Potenciometro > PIN ANALÓGICO A0
  IES SAN ISIDRO
  Dpto. Tecnología
