# Fritzing sketch id4368_steiner_0 (saved by Fritzing 0.9.0b)
circuit board: 10cm x 8cm
breadboards: 1

parts:
  D1 = Diode [package=diode-1n4148]
  D2 = Diode [package=diode-1n4148]
  D3 = Diode [package=diode-1n4148]
  D4 = Diode [package=diode-1n4148]
  D5 = Diode [package=diode-1n4148]
  D6 = Diode [package=diode-1n4148]
  D7 = Diode [package=diode-1n4148]
  D8 = Diode [package=diode-1n4148]
  Q2 = NPN-Transistor [package="TO92 [THT]"]
  Q3 = NPN-Transistor [package="TO92 [THT]"]
  C1 = Ceramic Capacitor [capacitance=4.7nF package="200 mil [THT, multilayer]"]
  C2 = Ceramic Capacitor [capacitance=4.7nF package="200 mil [THT, multilayer]"]
  C3 = Ceramic Capacitor [capacitance=4.7nF package="200 mil [THT, multilayer]"]
  R3 = Resistor [tolerance=±5% resistance=220 package=THT]
  R4 = Resistor [tolerance=±5% resistance=220 package=THT]
  R1 = Resistor [tolerance=±5% resistance=1k package=THT]
  R2 = Resistor [tolerance=±5% resistance=1k package=THT]
  R5 = Resistor [tolerance=±5% resistance=3.9k package=THT]
  R6 = Resistor [tolerance=±5% resistance=82 package=THT]
  Q4 = NPN-Transistor [package="TO92 [THT]"]
  C6 = Ceramic Capacitor [capacitance=100nF package="200 mil [THT, multilayer]"]
  Q5 = PNP-Transistor [package="TO92 [THT]"]
  R9 = Resistor [tolerance=±5% resistance=1k package=THT]
  R10 = Resistor [tolerance=±5% resistance=2.2k package=THT]
  D9 = Diode [package=diode-1n4148]
  D10 = Diode [package=diode-1n4148]
  R11 = Resistor [tolerance=±5% resistance=1k package=THT]
  R12 = Resistor [tolerance=±5% resistance=8.2k package=THT]
  R13 = Resistor [tolerance=±5% resistance=365 package=THT]
  R14 = Resistor [tolerance=±5% resistance=3.3m package=THT]
  R15 = Resistor [tolerance=±5% resistance=2.2k package=THT]
  R16 = Resistor [tolerance=±5% resistance=1.8k package=THT]
  J2 = female pin header, 2 pins [form="♀ (female)"]
  R17 = Resistor [tolerance=±5% resistance=47k package=THT]
  R18 = Resistor [tolerance=±5% resistance=47k package=THT]
  R19 = Resistor [tolerance=±5% resistance=47k package=THT]
  J3 = female pin header, 3 pins [form="♀ (female)"]
  R20 = Resistor [tolerance=±5% resistance=68k package=THT]
  C7 = Electrolytic Capacitor [capacitance=10µF package="100 mil [THT, electrolytic]"]
  J4 = female pin header, 2 pins [form="♀ (female)"]
  R21 = Resistor [tolerance=±5% resistance=220 package=THT]
  R22 = Resistor [tolerance=±5% resistance=220 package=THT]
  C8 = Electrolytic Capacitor [capacitance=10µF package="100 mil [THT, electrolytic]"]
  C9 = Electrolytic Capacitor [capacitance=10µF package="100 mil [THT, electrolytic]"]
  J5 = female pin header, 3 pins [form="♀ (female)"]
  J1 = female pin header, 6 pins [form="♀ (female)"]
  C10 = Electrolytic Capacitor [capacitance=150µF package="100 mil [THT, electrolytic]"]
  C11 = Electrolytic Capacitor [capacitance=150µF package="100 mil [THT, electrolytic]"]

nets:
  N1: D1.A, D2.C
  N2: D1.C, Q2.C, R3.Pin_1
  N3: D2.A, D3.C, C1.1
  N4: D3.A, D4.C
  N5: D4.A, D5.C, C2.1, C6.0
  N6: D5.A, D6.C
  N7: D6.A, D7.C, C3.1
  N8: D7.A, D8.C
  N9: D8.A, Q3.C, R4.Pin_1
  N10: Q2.E, Q3.E, R5.Pin_0
  N11: Q2.B, R17.Pin_0, R18.Pin_0, R19.Pin_0
  GND: Q3.B, C2.0, R3.Pin_0, R4.Pin_0, R1.Pin_0, R1.Pin_1, R10.Pin_1, R11.Pin_1, R15.Pin_1, J3.pin3, J4.pin1, C8.+, C9.-, J5.pin2, J1.pin1, C10.-, C11.+
  N12: C1.0, C3.0, R2.Pin_0, R2.Pin_1, R9.Pin_1, J1.pin2
  N13: R5.Pin_1, R6.Pin_1, C11.-
  -15V: R6.Pin_0, R21.Pin_0, C8.-
  N14: Q4.E, R10.Pin_0, D9.C, D10.A, R16.Pin_1
  N15: Q4.B, C6.1, R14.Pin_0
  N16: Q4.C, Q5.B
  N17: Q5.E, R11.Pin_0, R12.Pin_0, R13.Pin_1, C10.+
  N18: Q5.C, R9.Pin_0, D9.A, D10.C, J2.pin2, C7.+
  N19: R12.Pin_1, R14.Pin_1, R15.Pin_0
  15V: R13.Pin_0, R20.Pin_1, R22.Pin_0, C9.+
  N20: R16.Pin_0, J2.pin1
  N21: R17.Pin_1, J1.pin3
  N22: R18.Pin_1, J1.pin4
  N23: R19.Pin_1, J3.pin2
  N24: J3.pin1, R20.Pin_0
  N25: C7.-, J4.pin2
  N26: R21.Pin_1, J5.pin1
  N27: R22.Pin_1, J5.pin3

notes:
  Steiner (c)2014 GAVAGE
  out
  res
