# Fritzing sketch id4371_VD&C_1_0 (saved by Fritzing 0.9.2b)
breadboards: 1

parts:
  Part1 = Arduino Uno (Rev3)  # not connected
  Part2 = Memoire 1.0 - SD card log shield
  J1 = Screw terminal - 2 pins [package=THT]

nets:
  N1: Part2.A_IN_0, Part2.N$20, J1.pin2
  N2: Part2.GND, Part2.N$21, J1.pin1
