# Fritzing sketch id4373_VehiculoSensorMovil_0 (saved by Fritzing 0.8.3b)
breadboards: 1

parts:
  Arduino1 = Arduino
  M1 = DC Motor
  X1 = Sonar
  EDGY_motor_control1 = EDGY
  M2 = DC Motor
  EDGY_motor_control2 = EDGY
  M4 = Stepper Motor - Unipolar

nets:
  N1: Arduino1.D13, X1.connector2
  N2: Arduino1.D12, X1.connector1
  N3: Arduino1.D11, EDGY_motor_control2.A1out
  N4: Arduino1.D10, EDGY_motor_control2.B1out
  N5: Arduino1.D9, EDGY_motor_control2.A2out
  N6: Arduino1.D8, EDGY_motor_control2.B2out
  N7: Arduino1.D7, EDGY_motor_control1.B2
  N8: Arduino1.D6, EDGY_motor_control1.A2
  N9: Arduino1.D5, EDGY_motor_control1.B1
  N10: Arduino1.D4, EDGY_motor_control1.A1
  N11: M1.pin_1, EDGY_motor_control1.A2out
  N12: M1.pin_2, EDGY_motor_control1.B2out
  GND: X1.connector0, EDGY_motor_control1.GND, EDGY_motor_control2.GND
  N13: X1.connector3, EDGY_motor_control1.5V+, EDGY_motor_control2.5V+
  N14: EDGY_motor_control1.B1out, M2.pin_2
  N15: EDGY_motor_control1.A1out, M2.pin_1
  N16: EDGY_motor_control2.B1, M4.COMMON_2
  N17: EDGY_motor_control2.Speed1, M4.B
  N18: EDGY_motor_control2.A2, M4.C
  N19: EDGY_motor_control2.B2, M4.COMMON_1
  N20: EDGY_motor_control2.Speed2, M4.A
