# Fritzing sketch id4375_VentiPrint_0 (saved by Fritzing 0.8.5b)
circuit board: 8.24312cm x 5.4892cm
breadboards: 1

parts:
  Teensy_3_1 = Teensy 3.0
  IC1 = L293D [package=THT]
  Temp1 = LM35 Temperature Sensor [package="TO92 [THT]"]
  7805 = Voltage Regulator - 5V [package="TO220 [THT]"]
  V2 = DC Power [voltage=12V]
  Temp2 = LM35 Temperature Sensor [package="TO92 [THT]"]
  Motor1 = DC Motor
  Motor2 = DC Motor
  Opto = female pin header, 2 pins [form="♀ (female)"]
  J2 = female pin header, 7 pins [form="♀ (female)"]
  -12V+ = female pin header, 2 pins [form="♀ (female)"]
  Motor3 = DC Motor

nets:
  GND: Teensy_3_1.GND, IC1.0V, IC1.In_2, IC1.In_4, Temp1.GND, 7805.GND, V2.V-, Temp2.GND, Opto.pin1, J2.pin7, -12V+.pin1
  N1: Teensy_3_1.D2, Opto.pin2
  N2: Teensy_3_1.D3, IC1.Enable_1
  N3: Teensy_3_1.D4, IC1.In_1
  N4: Teensy_3_1.D5, IC1.Enable_2
  N5: Teensy_3_1.D6, IC1.In_3
  N6: Teensy_3_1.A0/D14, Temp1.Vout
  N7: Teensy_3_1.A1/D15, Temp2.Vout
  N8: Teensy_3_1.A5/D19, J2.pin6
  N9: Teensy_3_1.A6/D20, J2.pin5
  N10: Teensy_3_1.A7/D21, J2.pin4
  N11: Teensy_3_1.A8/D22, J2.pin3
  N12: Teensy_3_1.A9/D23, J2.pin2
  N13: Teensy_3_1.Vin, IC1.+V, Temp1.+Vs, 7805.output_voltage, Temp2.+Vs, J2.pin1
  N14: IC1.Out_1_(_Controlled_by_Enable_1_), Motor1.pin_2
  N15: IC1.Out_2_(_Controlled_by_Enable_1_), Motor1.pin_1
  N16: IC1.+Vmotor, 7805.input_voltage, V2.V+, -12V+.pin2
  N17: IC1.Out_3_(_Controlled_by_Enable_2_), Motor2.pin_2, Motor3.pin_1
  N18: IC1.Out_4_(_Controlled_by_Enable_2_), Motor2.pin_1, Motor3.pin_2

notes:
  [5V]
  [12V Einspeisung]
  [Oled]
  [Opto]
