# Fritzing sketch id437_file_0 (saved by Fritzing 0.8.3b)
breadboards: 1

parts:
  Componente1 = Arduino Uno (Rev3)
  LED1 = RGB LED (com. anode, rbg) [package="5 mm [THT]"]
  R1 = Resistor [tolerance=±5% resistance=220 package=THT]
  R2 = Photocell (LDR) [package=THT]
  R3 = Resistor [tolerance=±5% resistance=10k package=THT]
  S1 = Pushbutton [package=THT]
  R4 = Resistor [tolerance=±5% resistance=10k package=THT]

nets:
  N1: Componente1.A0, R2.pin_1, R3.Pin_0
  N2: Componente1.ICSP_MOSI, Componente1.D11_PWM/MOSI, LED1.red_cathode
  N3: Componente1.D9_PWM, LED1.green_cathode
  N4: Componente1.D10_PWM/SS, LED1.blue_cathode
  N5: Componente1.D2, S1.leg1, R4.Pin_1
  N6: Componente1.5V, R1.Pin_0, R2.pin_0, R4.Pin_0
  N7: Componente1.GND, R3.Pin_1, S1.leg0
  N8: LED1.common_anode, R1.Pin_1
