# Fritzing sketch id439_arduino_ldc_e_servomotor_0 (saved by Fritzing 0.7.12b)
breadboards: 1

parts:
  Arduino1 = Arduino
  LCD1 = LCD screen
  R1 = Rotary Potentiometer (Large) [maximum_resistance=100kΩ package=THT]
  R2 = Rotary Potentiometer (Large) [maximum_resistance=100kΩ package=THT]
  R3 = Rotary Potentiometer (Large) [maximum_resistance=100kΩ package=THT]
  J1 = Basic Servo

nets:
  N1: Arduino1.D12, J1.pulse
  N2: Arduino1.D9, LCD1.RS
  N3: Arduino1.D8, LCD1.E
  N4: Arduino1.D5, LCD1.DB4
  N5: Arduino1.D4, LCD1.DB5
  N6: Arduino1.D3, LCD1.DB6
  N7: Arduino1.D2, LCD1.DB7
  +5V: Arduino1.+5V, LCD1.VDD, R1.leg1, R2.leg1, R3.leg2, J1.vcc
  GND: Arduino1.GND, LCD1.VSS, LCD1.R/W, LCD1.LED-, R1.leg2, R2.leg2, R3.leg1, J1.gnd
  N8: Arduino1.A0, R3.wiper
  N9: LCD1.V0, R1.wiper
  N10: LCD1.LED+, R2.wiper
