# Fritzing sketch id43_Hymer_S_660_0 (saved by Fritzing 0.9.2b)
stripboards: 1

parts:
  U1 = Voltage Regulator - 5V [package="TO220 [THT]"]
  C3 = Electrolytic Capacitor [capacitance=100µF voltage=35V package="100 mil [THT, electrolytic]"]
  C4 = Electrolytic Capacitor [capacitance=100μF voltage=35V package="100 mil [THT, electrolytic]"]
  C6 = prefix0000
  C7 = prefix0000
  J1 = Screw terminal - 2 pins [package=THT]
  Onderdeel1 = Arduino Pro Mini v13
  FTDI1 = FTDI_Friend
  SW1 = prefix0000
  S1 = Pushbutton [package="[THT]"]
  S2 = Pushbutton [package="[THT]"]
  S3 = Toggle Switch [package=THT]
  R2 = Resistor [tolerance=±5% resistance=10k package=THT]  # not connected
  R4 = Resistor [tolerance=±5% resistance=10k package=THT]
  R6 = Resistor [tolerance=±5% resistance=10k package=THT]
  R7 = Resistor [tolerance=±5% resistance=10k package=THT]
  DHT1 = DHT11_Temperature_and_Humitidy_Sensor
  DHT2 = DHT11_Temperature_and_Humitidy_Sensor
  Onderdeel2 = richardbruneau00
  R8 = Resistor [tolerance=±5% resistance=10k package=THT]  # not connected
  LCD1 = LCD screen  # not connected

nets:
  N1: U1.input_voltage, C4.+, C7.connector0, Onderdeel1.VCC, FTDI1.connector3, R6.Pin_0, R7.Pin_1
  N2: U1.GND, C3.-, C4.-, C6.connector1, C7.connector1
  N3: U1.output_voltage, C3.+, C6.connector0, J1.pin1
  N4: J1.pin2, Onderdeel1.GND, FTDI1.connector1
  N5: Onderdeel1.D0/TX, FTDI1.connector5
  N6: Onderdeel1.D1/RX, FTDI1.connector4
  N7: Onderdeel1.D12/MISO, S1.Pin_4
  N8: Onderdeel1.D11_PWM/MOSI, S2.Pin_4
  N9: Onderdeel1.D10_PWM/SS, SW1.connector0, R7.Pin_0
  N10: Onderdeel1.D9_PWM, SW1.connector3
  N11: Onderdeel1.D8, DHT2.connector2
  N12: Onderdeel1.D7, DHT1.connector2
  N13: Onderdeel1.D6_PWM, S3.L1, R4.Pin_0
  N14: Onderdeel1.D5_PWM, Onderdeel2.connector12
  N15: Onderdeel1.D4, Onderdeel2.connector13

notes:
  12 Volt Car
  7805
  On/Off
  Min.
  Uur
  220Nf
  100µF
  Temp.
  In     Out
  + 5 volt Reg.
  PullUp
  Inside
  Outside
  Display
  SDA
  SCL
  This 1602 module has a
  IC2 Backpack
  FTDI-232
