# Fritzing sketch id4400_servo_scanner (saved by Fritzing 0.3.16b)
breadboards: 1

parts:
  Arduino1 = Arduino
  J1 = screw terminal, 3 pins
  J2 = Basic Servo
  R1 = Photocell (LDR) [package=THT]
  R2 = Resistor [resistance=1.5k package=THT]

nets:
  GND: Arduino1.GND, J1.pin1, J2.gnd, R1.pin_0
  N1: Arduino1.D9, J2.pulse
  +5V: Arduino1.+5V, J2.vcc
  N2: Arduino1.A1, J1.pin3, R1.pin_1, R2.Pin_0
