# Fritzing sketch id440_arduinoasisp (saved by Fritzing 0.6.4b)
breadboards: 1

parts:
  U1 = attiny85 [package=dip]
  C1 = Electrolytic Capacitor [capacitance=1µF package="100 mil [THT, electrolytic]"]
  Arduino1 = Arduino
  LED1 = LED - 5mm [color="Red (633nm)" package="5 mm [THT]"]

nets:
  N1: U1.Pin_1, Arduino1.D10
  N2: U1.Pin_3, LED1.anode
  N3: U1.Pin_4, U1.Pin_8, C1.+, Arduino1.GND, LED1.cathode
  N4: U1.Pin_5, Arduino1.D11
  N5: U1.Pin_6, Arduino1.D12
  N6: U1.Pin_7, Arduino1.D13
  N7: C1.-, Arduino1.RST
