# Fritzing sketch id4415_tape_taupe (saved by Fritzing 0.9.3b)
circuit board: 11.455cm x 6.75027cm
breadboards: 1

parts:
  Arduino_nano = Arduino Nano (Rev3.0)
  12v = Power plug
  LED1 = LED - 5mm [color="Red (633nm)" package="5 mm [THT]"]
  LED2 = LED - 5mm [color="Red (633nm)" package="5 mm [THT]"]
  LED3 = LED - 5mm [color="Red (633nm)" package="5 mm [THT]"]
  LED4 = LED - 5mm [color="Red (633nm)" package="5 mm [THT]"]
  LED5 = LED - 5mm [color="Red (633nm)" package="5 mm [THT]"]
  LED6 = LED - 5mm [color="Red (633nm)" package="5 mm [THT]"]
  LED7 = LED - 5mm [color="Red (633nm)" package="5 mm [THT]"]
  LED8 = LED - 5mm [color="Red (633nm)" package="5 mm [THT]"]
  LED9 = LED - 5mm [color="Red (633nm)" package="5 mm [THT]"]
  LED10 = LED - 5mm [color="Red (633nm)" package="5 mm [THT]"]
  LED11 = LED - 5mm [color="Red (633nm)" package="5 mm [THT]"]
  LED12 = LED - 5mm [color="Red (633nm)" package="5 mm [THT]"]
  LED13 = LED - 5mm [color="Red (633nm)" package="5 mm [THT]"]
  LED14 = LED - 5mm [color="Red (633nm)" package="5 mm [THT]"]
  LED15 = LED - 5mm [color="Red (633nm)" package="5 mm [THT]"]
  LED16 = LED - 5mm [color="Red (633nm)" package="5 mm [THT]"]
  R_2 = Resistor [tolerance=±5% resistance=220 package=THT]
  R_3 = Resistor [tolerance=±5% resistance=220 package=THT]
  R_4 = Resistor [tolerance=±5% resistance=220 package=THT]
  R_1 = Resistor [tolerance=±5% resistance=220 package=THT]
  R_5 = Resistor [tolerance=±5% resistance=220 package=THT]
  R_8 = Resistor [tolerance=±5% resistance=220 package=THT]
  R_7 = Resistor [tolerance=±5% resistance=220 package=THT]
  R_6 = Resistor [tolerance=±5% resistance=220 package=THT]
  R_9 = Resistor [tolerance=±5% resistance=220 package=THT]
  R_10 = Resistor [tolerance=±5% resistance=220 package=THT]
  R_13 = Resistor [tolerance=±5% resistance=220 package=THT]
  R_16 = Resistor [tolerance=±5% resistance=220 package=THT]
  R_15 = Resistor [tolerance=±5% resistance=220 package=THT]
  R_14 = Resistor [tolerance=±5% resistance=220 package=THT]
  R_12 = Resistor [tolerance=±5% resistance=220 package=THT]
  IC1 = IC, DIP package, 20 pins [chip_label=TPIC6B595]
  IC2 = IC, DIP package, 20 pins [chip_label=TPIC6B595]
  R_11 = Resistor [tolerance=±5% resistance=220 package=THT]

nets:
  N1: Arduino_nano.D10, IC1.pin12, IC2.pin12
  N2: Arduino_nano.D11/MOSI, IC2.pin3
  N3: Arduino_nano.D12/MISO, IC1.pin13, IC2.pin13
  GND: Arduino_nano.GND, 12v.GND, IC1.pin9, IC1.pin10, IC1.pin11, IC1.pin19, IC2.pin9, IC2.pin10, IC2.pin11, IC2.pin19
  N4: Arduino_nano.5V, IC1.pin2, IC1.pin8, IC2.pin2, IC2.pin8
  N5: 12v.VCC, LED1.anode, LED2.anode, LED3.anode, LED4.anode, LED5.anode, LED6.anode, LED7.anode, LED8.anode, LED9.anode, LED10.anode, LED11.anode, LED12.anode, LED13.anode, LED14.anode, LED15.anode, LED16.anode
  N6: LED1.cathode, R_1.Pin_0
  N7: LED2.cathode, R_2.Pin_0
  N8: LED3.cathode, R_3.Pin_0
  N9: LED4.cathode, R_4.Pin_0
  N10: LED5.cathode, R_5.Pin_0
  N11: LED6.cathode, R_6.Pin_0
  N12: LED7.cathode, R_7.Pin_0
  N13: LED8.cathode, R_8.Pin_0
  N14: LED9.cathode, R_9.Pin_0
  N15: LED10.cathode, R_10.Pin_0
  N16: LED11.cathode, R_11.Pin_0
  N17: LED12.cathode, R_12.Pin_0
  N18: LED13.cathode, R_13.Pin_0
  N19: LED14.cathode, R_14.Pin_0
  N20: LED15.cathode, R_15.Pin_0
  N21: LED16.cathode, R_16.Pin_0
  N22: R_2.Pin_1, IC1.pin16
  N23: R_3.Pin_1, IC1.pin15
  N24: R_4.Pin_1, IC1.pin14
  N25: R_1.Pin_1, IC1.pin17
  N26: R_5.Pin_1, IC2.pin17
  N27: R_8.Pin_1, IC2.pin14
  N28: R_7.Pin_1, IC2.pin15
  N29: R_6.Pin_1, IC2.pin16
  N30: R_9.Pin_1, IC1.pin4
  N31: R_10.Pin_1, IC1.pin5
  N32: R_13.Pin_1, IC2.pin4
  N33: R_16.Pin_1, IC2.pin7
  N34: R_15.Pin_1, IC2.pin6
  N35: R_14.Pin_1, IC2.pin5
  N36: R_12.Pin_1, IC1.pin7
  N37: IC1.pin3, IC2.pin18
  N38: IC1.pin6, R_11.Pin_1
