# Fritzing sketch id4418_TARDIS (saved by Fritzing 0.9.3b)
circuit board: 7.1cm x 4.4cm

parts:
  Open_Door_-_Static_Mode = SWITCH-SPST-2 [package=switch-spst-vertical]
  IR1 = TSOP312.., 314.. [package=THT]
  JP1 = Header 3 [package=1x03-1mm-ra]
  IR_RECEIVER = Header 3 [package=1x03-1mm-ra]
  JP3 = Header 3 [package=1x03-1mm-ra]
  POWER_KEY = Header 3 [package=1x03-1mm-ra]
  RELAY_LIGHT = RELAY [package=relay-g5q]
  LAMPIOTE = LED - 5mm [color="Red (633nm)" package="5 mm [THT]"]
  Power_plug1 = Power plug
  MODE = Square Pushbutton
  part = Raspberry Pi Zero
  LIGHT = Header 3 [package=1x03-1mm-ra]

nets (from the schematic view):
  N1: Open_Door_-_Static_Mode.O, JP3.1
  N2: Open_Door_-_Static_Mode.P, JP3.3
  N3: IR1.GND, JP1.1
  N4: IR1.Vs, JP1.3
  N5: IR1.Data, JP1.2
  N6: IR_RECEIVER.1, POWER_KEY.1, RELAY_LIGHT.COIL2, MODE.leg0, part.GND, LIGHT.3
  N7: IR_RECEIVER.2, part.GPIO4
  N8: IR_RECEIVER.3, part.3v3
  N9: POWER_KEY.3, part.GPIO27
  N10: RELAY_LIGHT.MAIN, LAMPIOTE.anode
  N11: RELAY_LIGHT.NC, Power_plug1.VCC
  N12: RELAY_LIGHT.COIL1, part.GPIO20
  N13: LAMPIOTE.cathode, Power_plug1.GND
  N14: MODE.leg1, part.GPIO17
  N15: part.GPIO16, LIGHT.1

notes:
  TARDIS V1
