# Fritzing sketch id441_Arduino_Control_Device_0 (saved by Fritzing 0.9.0b)
breadboards: 1

parts:
  Componente1 = Arduino Uno (Rev3)
  BUTTON1 = Arcade_Button__red
  BUTTON3 = Arcade_Button__green
  BUTTON4 = Arcade_Button__white
  R1 = Resistor [tolerance=±5% resistance=10k package=THT]
  R2 = Resistor [tolerance=±5% resistance=10k package=THT]
  R3 = Resistor [tolerance=±5% resistance=10k package=THT]
  R4 = Slide Potentiometer [maximum_resistance=100kΩ]

nets:
  N1: Componente1.A0, R4.wiper
  N2: Componente1.D2, BUTTON3.connector1, R1.Pin_1
  N3: Componente1.D3_PWM, BUTTON1.connector1, R2.Pin_1
  N4: Componente1.D4, BUTTON4.connector1, R3.Pin_1
  N5: Componente1.5V, R1.Pin_0, R2.Pin_0, R3.Pin_0, R4.leg1, R4.leg2
  N6: Componente1.GND, BUTTON1.connector2, BUTTON3.connector2, BUTTON4.connector2

notes:
  Slide Resistors
  500K (log)
  R1 = R2 = R3 = 10K
  Buttons
