# Fritzing sketch id4428_Untitled_Sketch_1_0 (saved by Fritzing 0.9.2b)
perfboards: 1

parts:
  U1 = 555 Timer [package="DIP8 [THT]"]  # not connected
  R1 = Resistor [tolerance=±5% resistance=220 package="0402 [SMD]"]  # not connected
  Q1 = TRANSISTOR_NPN [package=to-92]
  R2 = Resistor [tolerance=±5% resistance=220 package="0402 [SMD]"]
  R3 = Resistor [tolerance=±5% resistance=220 package="0402 [SMD]"]
  Q2 = PNP-Transistor [package="TO92 [THT]"]
  IC1 = Voltage Regulator [package=to220-igo]  # not connected
  D1 = Rectifier Diode [package="Melf DO-213 AA [SMD]"]
  VCC1 = Battery  # not connected
  R4 = Resistor [tolerance=±5% resistance=220 package="0402 [SMD]"]
  R5 = Temperature Sensor (Thermistor) [thermistor_type=NTC package=THT]  # not connected
  R6 = Resistor [tolerance=±5% resistance=220 package="0402 [SMD]"]
  LED1 = smd LED [color="Red (633nm)" package="0805 [SMD]"]
  R7 = Resistor [tolerance=±5% resistance=220 package="0805 [SMD]"]
  R8 = Resistor [tolerance=±5% resistance=220 package="0603 [SMD]"]
  U2 = 555 Timer [package="DIP8 [THT]"]  # not connected
  R9 = Resistor [tolerance=±5% resistance=220 package=THT]
  D2 = Diode [package=diode-1n4148]  # not connected
  D3 = Rectifier Diode [part_number=1N4001 package="300 mil [THT]"]
  R10 = Rotary Potentiometer (Small) [maximum_resistance=100kΩ package=THT]  # not connected
  C1 = Capacitor [package=cap-pth-small2]
  C2 = Capacitor [package=cap-pth-small2]
  R11 = Resistor [tolerance=±5% resistance=220 package=THT]
  LED2 = LED - 3mm [color="Red (633nm)" package="3 mm [THT]"]
  LED3 = LED - 3mm [color="Red (633nm)" package="3 mm [THT]"]
  LED4 = LED - 3mm [color="Red (633nm)" package="3 mm [THT]"]
  LED5 = LED - 3mm [color="Red (633nm)" package="3 mm [THT]"]
  LED6 = LED - 3mm [color="Red (633nm)" package="3 mm [THT]"]
  LED7 = LED - 3mm [color="Red (633nm)" package="3 mm [THT]"]
  R12 = Resistor [tolerance=±5% resistance=220 package=THT]
  Q3 = TRANSISTOR_NPN [package=to-92-ammo]

nets:
  N1: Q1.E, R2.Pin_1
  N2: R2.Pin_0, R3.Pin_1
  N3: Q2.B, D1.cathode
  N4: D1.anode, R9.Pin_0, R11.Pin_1
  N5: R4.Pin_0, R6.Pin_1
  N6: R6.Pin_0, LED1.anode
  N7: R7.Pin_1, R8.Pin_1
  N8: R9.Pin_1, D3.anode
  N9: C1.2, C2.2, Q3.C
  N10: R11.Pin_0, LED2.anode, LED3.anode, LED4.anode, LED5.anode, LED6.anode, LED7.anode
  N11: LED2.cathode, LED3.cathode, LED4.cathode, LED5.cathode, LED6.cathode, LED7.cathode, Q3.E
  N12: R12.Pin_1, Q3.B
