# Fritzing sketch id442_Untitled_Sketch_0 (saved by Fritzing 0.9.2b)

parts:
  U1 = RELAY [package=relay-t9a-2]
  HCMS-29XX1 = HCMS-29xx
  U2 = LIPO-2000mAh [package=lipo-2000]
  U3 = Luxeon LED [package=luxeon]
  Part2 = Arduino Nano (Rev3.0)
  U4 = EM408_CON [package=em408_con]

nets:
  N1: U1.COIL1, U3.S
  N2: U1.MAIN, U2.+
  N3: U1.NC, Part2.D4
  N4: HCMS-29XX1.VLED, Part2.GND
  N5: HCMS-29XX1.RS, Part2.3V3
  N6: HCMS-29XX1.SEL, Part2.D6
  N7: U2.-, U3.A
  N8: Part2.D7, U4.EN

notes:
  5v Relay
  8bit Neopixel
  1w PowerLed
  RC Receiver
