# Fritzing sketch id4430_Angelo1_0 (saved by Fritzing 0.7.11b)
breadboards: 1

parts:
  S1 = Pushbutton [package="[THT]"]
  LED1 = LED - 5mm [color="Red (633nm)" package="5 mm [THT]"]
  Arduino_UNO = Arduino
  R1 = Trimmer Potentiometer [maximum_resistance=10kΩ package=THT]
  R2 = Resistor [tolerance=±5% resistance=220 package=THT]
  R3 = Rotary Potentiometer (Small) [maximum_resistance=100kΩ]
  J1 = Piezo Speaker
  LCD1_20x4 = lcd-GDM1602K.fzp

nets:
  N1: S1.Pin_1, S1.Pin_2, Arduino_UNO.D2
  GND: S1.Pin_3, S1.Pin_4, Arduino_UNO.GND, R1.leg1, R2.Pin_0, R3.leg1, J1.pin1, LCD1_20x4.connector0, LCD1_20x4.connector4, LCD1_20x4.connector14
  N2: LED1.cathode, Arduino_UNO.D4
  N3: LED1.anode, R2.Pin_1
  N4: Arduino_UNO.D12, LCD1_20x4.connector13
  N5: Arduino_UNO.D11, LCD1_20x4.connector12
  N6: Arduino_UNO.D10, LCD1_20x4.connector11
  N7: Arduino_UNO.D9, LCD1_20x4.connector10
  N8: Arduino_UNO.D8, LCD1_20x4.connector5
  N9: Arduino_UNO.D7, LCD1_20x4.connector3
  N10: Arduino_UNO.D3, J1.pin2
  5V: Arduino_UNO.+5V, R1.leg2, R3.leg2, LCD1_20x4.connector1, LCD1_20x4.connector15
  N11: Arduino_UNO.A0, R3.wiper
  N12: R1.wiper, LCD1_20x4.connector2

notes:
  Teaching circuit 1, Test LCD 20x4, led, buzzer, switch, 1.0
  WARNING !
  some LCD have LED+/LED- pins swapped, check datasheet or board
  Not tested, check!
