# Fritzing sketch id4432_VideopacG7000_composite_mod_0 (saved by Fritzing 0.9.2b)
perfboards: 1

parts:
  R1 = Resistor [tolerance=±5% resistance=5.6k package=THT]
  R2 = Resistor [tolerance=±5% resistance=3.9k package=THT]
  R3 = Resistor [tolerance=±5% resistance=270 package=THT]
  R4 = Resistor [tolerance=±5% resistance=470 package=THT]
  R5 = Resistor [tolerance=±5% resistance=220 package=THT]
  R6 = Resistor [tolerance=±5% resistance=1k package=THT]
  R7 = Resistor [tolerance=±5% resistance=75 package=THT]
  C2 = Electrolytic Capacitor [capacitance=10µF package="100 mil [THT, electrolytic]"]
  J1 = female pin header, 1 pin [form="♀ (female)" part_number="Video output"]
  J3 = female pin header, 1 pin [form="♀ (female)" part_number="Audio output"]
  J4 = female pin header, 1 pin [form="♀ (female)" part_number="Audio input"]
  R8 = Resistor [tolerance=±5% resistance=3.3k package=THT]
  R9 = Resistor [tolerance=±5% resistance=1.2k package=THT]
  J2 = female pin header, 1 pin [form="♀ (female)" part_number="Video input"]
  C1 = Electrolytic Capacitor [capacitance=1µF package="100 mil [THT, electrolytic]"]
  D1 = Rectifier Diode [part_number=1N4001 package="300 mil [THT]"]
  Q1 = NPN-Transistor [part_number=BC548 package="TO92 [THT]"]
  Q2 = PNP-Transistor [part_number=BC558 package="TO92 [THT]"]
  Q3 = NPN-Transistor [part_number=BC548 package="TO92 [THT]"]

nets:
  5V: R1.Pin_0, R3.Pin_0, Q2.E, Q3.C
  N1: R1.Pin_1, R2.Pin_0, C2.+, D1.anode
  GND: R2.Pin_1, R5.Pin_1, R6.Pin_1, C2.-, R9.Pin_1
  N2: R3.Pin_1, Q1.C, Q2.B
  N3: R4.Pin_0, Q2.C, Q3.B
  N4: R4.Pin_1, R5.Pin_0, Q1.E
  N5: R6.Pin_0, R7.Pin_0, Q3.E
  N6: R7.Pin_1, J1.pin1
  N7: J3.pin1, R8.Pin_1, R9.Pin_0
  N8: J4.pin1, R8.Pin_0
  N9: J2.pin1, C1.+
  N10: C1.-, D1.cathode, Q1.B
