# Fritzing sketch id4434_viessman___opto_link___PCB_0 (saved by Fritzing 0.9.1b)
circuit board: 3.68803cm x 2.84261cm
stripboards: 1

parts:
  R2 = Resistor [tolerance=±10% resistance=330 package=THT]
  R1 = Resistor [tolerance=±5% resistance=15k package=THT]
  Q1 = NPN-Transistor [package="TO92 [THT]"]
  D1 = LTE-302 [package=lte-302]
  R5 = Resistor [tolerance=±5% resistance=15k package=THT]
  Q2 = OFT-generic-3mm
  J1 = male pin header, 4 pins [form="♂ (male)"]
  Q3 = NPN-Transistor [package="TO92 [THT]"]
  R7 = Resistor [tolerance=±5% resistance=15k package=THT]

nets:
  N1: R2.Pin_0, D1.C
  GND: R2.Pin_1, J1.pin1, Q3.E, R7.Pin_1
  N2: R1.Pin_0, J1.pin4
  N3: R1.Pin_1, Q1.B
  N4: Q1.E, D1.A
  5V: Q1.C, R5.Pin_0, Q2.connector1, J1.pin2
  N5: R5.Pin_1, J1.pin3, Q3.C
  N6: Q2.connector0, Q3.B, R7.Pin_0

notes:
  GND 5V  TX  RX
  R1
  R2
  R5
  R7
  D1
  Q1
  Q2
  TX
  RX
  Viessman optolink-TTL coupler
  Q3
  +5V
  GND
  TTL
  Viessman
  Marc Quinton
  Fritzing
  made with
  V
  optolink
  Receiver
  Transmitter
  optolink - TTL - v1.0
  CBE
  +
