# Fritzing sketch id4436_VincularBT_0 (saved by Fritzing 0.9.3b)
breadboards: 1

parts:
  Componente1 = Bluetooth HC-05 Macho
  Componente2 = Arduino Uno (Rev3)

nets:
  N1: Componente1.TXD, Componente2.D0/RX
  N2: Componente1.RXD, Componente2.D1/TX
  VCC: Componente1.VCC, Componente2.3V3
  GND: Componente1.GND, Componente2.GND
