# Fritzing sketch id4437_Port_Virtuel_0 (saved by Fritzing 0.9.2b)
breadboards: 1

parts:
  Composant1 = Arduino Uno (Rev3)
  VCC1 = Battery block 9V  # not connected
  S1 = Pushbutton [package="[THT]"]
  S2 = Pushbutton [package="[THT]"]
  S3 = Pushbutton [package="[THT]"]
  LED1 = RGB LED (com. cathode, rgb) [package="5 mm [THT]"]
  LED2 = LED - 5mm [color="Blue (505nm)" package="5 mm [THT]"]
  LED3 = LED - 5mm [color="Blue (505nm)" package="5 mm [THT]"]
  LED4 = LED - 5mm [color="Blue (505nm)" package="5 mm [THT]"]
  R1 = Resistor [tolerance=±5% resistance=220 package=THT]
  R3 = Resistor [tolerance=±5% resistance=10k package=THT]
  R4 = Resistor [tolerance=±5% resistance=10k package=THT]
  R5 = Resistor [tolerance=±5% resistance=10k package=THT]
  R6 = Resistor [tolerance=±5% resistance=220 package=THT]
  R7 = Resistor [tolerance=±5% resistance=220 package=THT]
  R8 = Resistor [tolerance=±5% resistance=220 package=THT]

nets:
  N1: Composant1.D8, LED4.anode
  N2: Composant1.D9_PWM, LED1.red_anode
  N3: Composant1.D10_PWM/SS, LED1.blue_anode
  N4: Composant1.D2, S1.Pin_3, S1.Pin_4
  N5: Composant1.D3_PWM, S2.Pin_3, S2.Pin_4
  N6: Composant1.D4, S3.Pin_3, S3.Pin_4
  N7: Composant1.D6_PWM, LED2.anode
  N8: Composant1.D7, LED3.anode
  N9: Composant1.GND, R1.Pin_1, R3.Pin_1, R4.Pin_1, R6.Pin_1, R7.Pin_1, R8.Pin_1
  N10: S1.Pin_1, S1.Pin_2, R4.Pin_0
  N11: S2.Pin_1, S2.Pin_2, R5.Pin_0
  N12: S3.Pin_1, S3.Pin_2, R3.Pin_0
  N13: LED1.common_cathode, R1.Pin_0
  N14: LED2.cathode, R8.Pin_0
  N15: LED3.cathode, R6.Pin_0
  N16: LED4.cathode, R7.Pin_0
