# Fritzing sketch id4438_VL53L0X_Lidar_Connections_0 (saved by Fritzing 0.9.3b)
breadboards: 2

parts:
  U1 = RJ45 Jack [package=rj45-8]
  U2 = RJ45 Jack [package=rj45-8]
  Part1 = adafruit [part_number="Adafruit #3317"]
  Part2 = Arduino Uno (Rev3)
  U3 = RJ45 Jack [package=rj45-8]
  U4 = RJ45 Jack [package=rj45-8]
  Part3 = adafruit [part_number="Adafruit #3317"]

nets:
  N1: U1.5, U2.5, Part1.connector16, Part2.A4/SDA
  N2: U1.6, U1.7, U2.6, Part1.connector15, Part2.A5/SCL
  N3: Part1.connector10, Part2.5V
  N4: Part1.connector12, Part2.GND
  N5: Part1.connector14, Part2.D2
  N6: U3.5, U4.5, Part3.connector16
  N7: U3.6, U3.7, U4.6, Part3.connector15
