# Fritzing sketch id4439_Proto_0 (saved by Fritzing 0.9.2b)
breadboards: 1

parts:
  Q1 = Basic FET N-Channel [package="TO220 [THT]"]  # not connected
  U2 = OP482 - Low Power, High Speed JFET Quad Operational Amplifier [part_number=OP482]  # not connected
  Q2 = TRANSISTOR_NPN [package=to-92]
  C1 = Tantalum Capacitor [capacitance="1 μF" package="C 6032 [SMD, tantalum]"]
  Pre-Assembled_Female_BNC1 = Pre-Assembled Female BNC
  J1 = Power Jack [package=power_jack_slot]
  U1 = Voltage Regulator - 5V [package="TO220 [THT]"]
  U3 = Luxeon LED [package=luxeon]  # not connected

nets:
  N1: Q2.B, C1.-
  N2: C1.+, Pre-Assembled_Female_BNC1.PRB
  GND: Pre-Assembled_Female_BNC1.GND, J1.GND, U1.GND
  N3: J1.PWR, U1.input_voltage
