# Fritzing sketch id4440_B_V_LED_0 (saved by Fritzing 0.9.3b)
breadboards: 1

parts:
  LED1 = LED - 3mm [color="Blue (505nm)" package="3 mm [THT]"]
  LED2 = LED - 3mm [color="White (4500K)" package="3 mm [THT]"]
  LED3 = LED - 3mm [color="Red (635nm)" package="3 mm [THT]"]
  LED4 = LED - 3mm [color="Yellow (592nm)" package="3 mm [THT]"]
  LED5 = LED - 3mm [color="Green (565nm)" package="3 mm [THT]"]
  R1 = Resistor [tolerance=±5% resistance=220 package=THT]
  R2 = Resistor [tolerance=±5% resistance=220 package=THT]
  R3 = Resistor [tolerance=±5% resistance=220 package=THT]
  R4 = Resistor [tolerance=±5% resistance=220 package=THT]
  R5 = Resistor [tolerance=±5% resistance=220 package=THT]
  Part1 = Arduino Uno (Rev3)
  Part2 = Bluetooth HC-05 Macho

nets:
  N1: LED1.cathode, R5.Pin_0
  N2: LED1.anode, Part1.D5_PWM
  N3: LED2.cathode, R4.Pin_0
  N4: LED2.anode, Part1.D6_PWM
  N5: LED3.cathode, R3.Pin_0
  N6: LED3.anode, Part1.D7
  N7: LED4.cathode, R2.Pin_0
  N8: LED4.anode, Part1.D8
  N9: LED5.anode, Part1.D9_PWM
  GND: R1.Pin_1, R2.Pin_1, R3.Pin_1, R4.Pin_1, R5.Pin_1, Part1.GND, Part2.GND
  N10: Part1.D2, Part2.RXD
  N11: Part1.D3_PWM, Part2.TXD
  5V: Part1.5V, Part2.VCC

notes:
  Blue Wire - Blue LED
  White Wire - White LED
  Red Wire - Red LED
  Yellow Wire - Yellow LED
  Green Wire - Green LED
  Black Wire - Ground
  light Blue Wire -RX
  Purple Wire - TX
  Orange Wire - VCC (+5 vott)
