# Fritzing sketch id4441_Voltage_Divider_0 (saved by Fritzing 0.9.3b)
breadboards: 1

parts:
  VCC1 = Battery
  R1 = Resistor [tolerance=±5% resistance=10k package="2512 [SMD]"]
  R2 = Resistor [tolerance=±5% resistance=1k package="2512 [SMD]"]

nets:
  N1: VCC1.-, R1.Pin_0, R2.Pin_1
  N2: VCC1.+, R2.Pin_0

notes:
  Vout = 8.16
