# Fritzing sketch id4442_divisor_0 (saved by Fritzing 0.8.7b)
breadboards: 1

parts:
  R1 = Resistor [tolerance=±5% resistance=100 package=THT]
  R2 = Resistor [tolerance=±5% resistance=100 package=THT]
  VCC1 = Battery block 9V

nets:
  N1: R1.Pin_0, VCC1.+
  N2: R1.Pin_1, R2.Pin_0
  GND: R2.Pin_1
