# Fritzing sketch id4444_Voltage_Regulator_v1.1_0 (saved by Fritzing 0.9.3b)
circuit board: 3cm x 3cm
breadboards: 1

parts:
  LED1 = smd LED [color="Red (633nm)" package="1206 [SMD]"]
  3_3v = female pin header, 2 pins [form="♀ (female)"]
  5v = female pin header, 2 pins [form="♀ (female)"]
  Power = Power plug
  D1 = Diode [package=smb-diode]
  R1 = Resistor [tolerance=±5% resistance=470 package="1206 [SMD]"]
  C10 = Ceramic Capacitor [capacitance=0.1µF package="1206 [SMD, multilayer]"]
  C9 = Ceramic Capacitor [capacitance=0.1µF package="1206 [SMD, multilayer]"]
  C8 = Ceramic Capacitor [capacitance=0.1µF package="1206 [SMD, multilayer]"]
  C5 = Electrolytic Capacitor [capacitance=100μF voltage=16V package="1010 [SMD, electrolytic]"]
  LM1117_3_3v = Voltage Regulator LM1117 [package=sot223]
  LM1117_5v = Voltage Regulator LM1117 [package=sot223]

nets:
  GND: LED1.cathode, 5v.pin2, Power.GND, C9.1, C8.1, C5.-, LM1117_5v.ADJ
  N1: LED1.anode, R1.Pin_0
  N2: 3_3v.pin1, C10.0, LM1117_3_3v.OUT
  N3: 3_3v.pin2, C10.1, LM1117_3_3v.ADJ
  N4: 5v.pin1, C9.0, LM1117_3_3v.IN
  N5: Power.VCC, D1.A
  N6: D1.C, C8.0, LM1117_5v.IN
  N7: R1.Pin_1, C5.+, LM1117_5v.OUT
