# Fritzing sketch id4445_VoltageRegulator5V_0 (saved by Fritzing 0.9.0b)
breadboards: 1

parts:
  U1 = Voltage Regulator - 5V [package="DPak [SMD]"]
  1uF = prefix0000
  9V = BC9VPC [package=bc9vpc]
  100uF = Capacitor Polarized [package=cpol-radial-100uf-25v]
  On/Off = SWITCH_SPDT [package=kps-1290]

nets:
  N1: U1.input_voltage, 100uF.+, On/Off.S
  GND: U1.GND, 1uF.connector0, 9V.V-, 100uF.-
  5V: U1.output_voltage, 1uF.connector1
  N2: 9V.V+, On/Off.P
