# Fritzing sketch id4446_potvol_0 (saved by Fritzing 0.9.2b)
circuit board: 4.26728cm x 4.16838cm

parts:
  Componente1 = Arduino Nano (Rev3.0)
  U1 = POT [package=pot_mammoth]

nets:
  N1: Componente1.GND, U1.E
  N2: Componente1.5V, U1.S
  N3: Componente1.A0, U1.A
