# Fritzing sketch id4447_AnalogdataSdWriteRead_0 (saved by Fritzing 0.9.3b)
breadboards: 1

parts:
  パーツ1 = Arduino Uno (Rev3)
  C1 = Electrolytic Capacitor [capacitance=47µF package="100 mil [THT, electrolytic]"]
  C2 = Ceramic Capacitor [capacitance=100nF package="100 mil [THT, multilayer]"]
  Regulator3_3V = Voltage Regulator - 3.3V [package="TO220 [THT]"]
  Logic_henkan = IC, DIP package, 20 pins [chip_label=LogicHenkanFXMA108]
  microSD = IC, SIP package, 10 pins [chip_label=miicroSD]
  LED1 = LED - 5mm [color="Red (633nm)" package="5 mm [THT]"]
  R2 = Resistor [tolerance=±5% resistance=550 package=THT]
  R3 = Trimmer Potentiometer [maximum_resistance=10kΩ package=THT]
  R1 = Resistor [tolerance=±5% resistance=10k package=THT]
  IC1 = IC, DIP package, 14 pins [chip_label="74HC14AP_Schmitt trigger"]
  S1 = Pushbutton [package="[THT]"]
  R4 = Resistor [tolerance=±5% resistance=10k package=THT]
  R5 = Resistor [tolerance=±5% resistance=10k package=THT]
  C3 = Ceramic Capacitor [capacitance=0.1µF package="100 mil [THT, multilayer]"]

nets:
  N1: パーツ1.A0, R3.wiper
  N2: パーツ1.D11_PWM/MOSI, Logic_henkan.pin8
  N3: パーツ1.D12/MISO, microSD.pin7
  N4: パーツ1.D13/SCK, Logic_henkan.pin9
  N5: パーツ1.D2, IC1.pin2
  N6: パーツ1.D4, Logic_henkan.pin7
  N7: パーツ1.D5_PWM, LED1.anode
  N8: パーツ1.5V, C2.0, Regulator3_3V.input_voltage, Logic_henkan.pin1, R3.leg2, IC1.pin14, R4.Pin_0
  GND: パーツ1.GND, C1.-, C2.1, Regulator3_3V.GND, Logic_henkan.pin11, microSD.pin6, R2.Pin_0, R3.leg1, R1.Pin_0, IC1.pin7, S1.Pin_3, S1.Pin_4, C3.0
  N9: C1.+, Regulator3_3V.output_voltage, Logic_henkan.pin20, microSD.pin4
  N10: Logic_henkan.pin10, R1.Pin_1
  N11: Logic_henkan.pin12, microSD.pin5
  N12: Logic_henkan.pin13, microSD.pin3
  N13: Logic_henkan.pin14, microSD.pin2
  N14: LED1.cathode, R2.Pin_1
  N15: IC1.pin1, R5.Pin_0, C3.1
  N16: S1.Pin_1, S1.Pin_2, R4.Pin_1, R5.Pin_1
