# Fritzing sketch id4449_Pet_Project_2_0 (saved by Fritzing 0.9.2b)
breadboards: 1

parts:
  Part1 = Arduino Uno (Rev3)
  J1 = Basic Servo [part_number="Servo Y"]  # not connected
  R1 = Photocell (LDR) [package=THT]
  R2 = Resistor [tolerance=±5% resistance=220 package=THT]
  J2 = Basic Servo [part_number="Servo X"]

nets:
  N1: Part1.A0, R1.pin_1, R2.Pin_1
  N2: Part1.D9_PWM, J2.pulse
  5V: Part1.5V, R2.Pin_0, J2.vcc
  GND: Part1.GND, R1.pin_0, J2.gnd
