# Fritzing sketch id444_Solenoid_Arduino_0 (saved by Fritzing 0.8.3b)
breadboards: 1

parts:
  Part1 = Arduino Uno (Rev3)
  VCC1 = Battery block 9V
  VCC2 = Battery block 9V
  Q1 = NPN-Transistor [part_number=TIP120 package="TO92 [THT]"]
  R1 = Resistor [tolerance=±5% resistance=1k package=THT]
  L1 = Solenoid
  D1 = Rectifier Diode [part_number=1N4001 package="300 mil [THT]"]

nets:
  N1: Part1.ICSP_SCK, Part1.D13/SCK, R1.Pin_1
  N2: Part1.GND, VCC2.-, Q1.C
  N3: VCC1.-, VCC2.+
  N4: VCC1.+, L1.pin2, D1.cathode
  N5: Q1.E, R1.Pin_0
  N6: Q1.B, L1.pin1, D1.anode

notes:
  Arduino-powered Solenoid:
  http://www.instructables.com/id/Controlling-solenoids-with-arduino/
