# Fritzing sketch id4450_vume_0 (saved by Fritzing 0.7.4b)
breadboards: 1

parts:
  LED1 = LED - 5mm [color="Green (555nm)" package="5 mm [THT]"]
  LED2 = LED - 5mm [color="Green (555nm)" package="5 mm [THT]"]
  LED3 = LED - 5mm [color="Yellow (592nm)" package="5 mm [THT]"]
  LED4 = LED - 5mm [color="Yellow (592nm)" package="5 mm [THT]"]
  LED5 = LED - 5mm [color="Yellow (595nm)" package="5 mm [THT]"]
  LED6 = LED - 5mm [color="Yellow (595nm)" package="5 mm [THT]"]
  LED7 = LED - 5mm [color="Green (555nm)" package="5 mm [THT]"]
  LED8 = LED - 5mm [color="Green (555nm)" package="5 mm [THT]"]
  LED9 = LED - 5mm [color="Yellow (595nm)" package="5 mm [THT]"]
  LED10 = LED - 5mm [color="Red (633nm)" package="5 mm [THT]"]
  LED11 = LED - 5mm [color="Red (633nm)" package="5 mm [THT]"]
  Nano1 = Arduino Nano v2.3
  R3 = Resistor [tolerance=±5% resistance=470 package=THT]
  R5 = Resistor [tolerance=±5% resistance=470 package=THT]
  R6 = Resistor [tolerance=±5% resistance=470 package=THT]
  R7 = Resistor [tolerance=±5% resistance=470 package=THT]
  R8 = Resistor [tolerance=±5% resistance=470 package=THT]
  R9 = Resistor [tolerance=±5% resistance=470 package=THT]
  R4 = Resistor [tolerance=±5% resistance=470 package=THT]
  R10 = Resistor [tolerance=±5% resistance=470 package=THT]
  R11 = Resistor [tolerance=±5% resistance=470 package=THT]
  R12 = Resistor [tolerance=±5% resistance=470 package=THT]
  R13 = Resistor [tolerance=±5% resistance=470 package=THT]
  MIC1 = Microphone

nets:
  N1: LED1.cathode, LED2.cathode, LED3.cathode, LED4.cathode, LED5.cathode, LED6.cathode, LED7.cathode, LED8.cathode, LED9.cathode, LED10.cathode, LED11.cathode, Nano1.VIN
  N2: LED1.anode, R13.Pin_1
  N3: LED2.anode, R10.Pin_1
  N4: LED3.anode, R9.Pin_1
  N5: LED4.anode, R8.Pin_1
  N6: LED5.anode, R6.Pin_1
  N7: LED6.anode, R7.Pin_1
  N8: LED7.anode, R12.Pin_1
  N9: LED8.anode, R11.Pin_1
  N10: LED9.anode, R3.Pin_1
  N11: LED10.anode, R5.Pin_1
  N12: LED11.anode, R4.Pin_1
  N13: Nano1.D2, R13.Pin_0
  N14: Nano1.D3, R10.Pin_0
  N15: Nano1.D4, R12.Pin_0
  N16: Nano1.D5, R11.Pin_0
  N17: Nano1.D6, R9.Pin_0
  N18: Nano1.D7, R8.Pin_0
  N19: Nano1.D8, R6.Pin_0
  N20: Nano1.D9, R7.Pin_0
  N21: Nano1.D10, R3.Pin_0
  N22: Nano1.D11, R5.Pin_0
  N23: Nano1.D12, R4.Pin_0
  N24: Nano1.A2, MIC1.pin2
  N25: Nano1.A1, MIC1.pin1
