# Fritzing sketch id4451_VuMeter.TLC5940.Mic.LED_0 (saved by Fritzing 0.7.12b)
breadboards: 1

parts:
  Arduino2 = Arduino
  IC2 = IC, DIP package, 28 pins [chip_label=TLC5940 spacing=300mil]
  R3 = Resistor [tolerance=±5% resistance=10k package=THT]
  R4 = Resistor [tolerance=±5% resistance=2.2k package=THT]
  LED2 = LED - 5mm [color="Green (555nm)" package="5 mm [THT]"]
  LED3 = LED - 5mm [color="Red (633nm)" package="5 mm [THT]"]
  LED4 = LED - 5mm [color="Red (633nm)" package="5 mm [THT]"]
  LED5 = LED - 5mm [color="Red (633nm)" package="5 mm [THT]"]
  LED6 = LED - 5mm [color="Red (633nm)" package="5 mm [THT]"]
  LED7 = LED - 5mm [color="Red (633nm)" package="5 mm [THT]"]
  LED9 = LED - 5mm [color="Green (555nm)" package="5 mm [THT]"]
  LED10 = LED - 5mm [color="Yellow (595nm)" package="5 mm [THT]"]
  MIC1 = Microphone
  R5 = Resistor [tolerance=±5% resistance=10k package=THT]

nets:
  N1: Arduino2.D13, IC2.pin25
  N2: Arduino2.D11, IC2.pin26
  N3: Arduino2.D10, IC2.pin23, R3.Pin_0
  N4: Arduino2.D9, IC2.pin24
  N5: Arduino2.D3, IC2.pin18
  N6: Arduino2.+5V, IC2.pin19, IC2.pin21, R3.Pin_1, LED2.cathode, LED3.cathode, LED4.cathode, LED5.cathode, LED6.cathode, LED7.cathode, LED9.cathode, LED10.cathode, MIC1.pin2
  N7: Arduino2.GND, IC2.pin22, IC2.pin27, R4.Pin_1, R5.Pin_1
  N8: Arduino2.A5, MIC1.pin1, R5.Pin_0
  N9: IC2.pin1, LED9.anode
  N10: IC2.pin6, LED10.anode
  N11: IC2.pin11, LED7.anode
  N12: IC2.pin12, LED6.anode
  N13: IC2.pin13, LED5.anode
  N14: IC2.pin14, LED4.anode
  N15: IC2.pin15, LED3.anode
  N16: IC2.pin20, R4.Pin_0
  N17: IC2.pin28, LED2.anode

notes:
  Fill In all 16 LEDS.
  Using a combination of Green, Yellow and Red will improve the visual result of the VuMeter.
  The mic is not very sensitive. Perhaps incorporating an OpAmp to increase signal will improve performance?
  Sketch based on existing TLC5940 sketch found here:
  http://fritzing.org/projects/tlc5940-and-arduino/
  Arduino Code found in programming window:
  Window->Open Programming window
