# Fritzing sketch id4452_vusb_arduino_minimalshield_0 (saved by Fritzing 0.8.6b)
breadboards: 1

parts:
  Arduino1 = Arduino Uno (Rev3)
  S1 = Pushbutton [package=THT]
  R1 = Resistor [tolerance=±5% resistance=10k package=THT]
  CONN1 = USB connector [package=THT]
  D1 = Zener Diode [part_number=1N4732A breakdown_voltage=3.6V package="300 mil [THT]"]
  D2 = Zener Diode [part_number=1N4732A breakdown_voltage=3.6V package="300 mil [THT]"]
  R2 = Resistor [tolerance=±5% resistance=1.5k package=THT]
  R3 = Resistor [tolerance=±5% resistance=68 package=THT]
  R4 = Resistor [tolerance=±5% resistance=68 package=THT]

nets:
  GND: Arduino1.GND, R1.Pin_1, CONN1.GND, CONN1.chassis5, CONN1.chassis6, D1.cathode, D2.cathode
  N1: Arduino1.D12/MISO, S1.leg0, R1.Pin_0
  N2: Arduino1.D2, R3.Pin_0
  N3: Arduino1.D4, R4.Pin_0
  5V: Arduino1.5V, S1.leg1, CONN1.5V, R2.Pin_0
  N4: CONN1.d-, D2.anode, R2.Pin_1, R4.Pin_1
  N5: CONN1.d+, D1.anode, R3.Pin_1

notes:
  here you see how to attach all components to an Arduino. together with the vusb library it'll show up as an USB-Keyboard.
  Related examples:
  http://code.rancidbacon.com/ProjectLogArduinoUSB
  Sourcecode:
  https://code.google.com/p/vusb-for-arduino/source/browse/#hg%2Flibraries
