# Fritzing sketch id4453_PROJECTE_ANDIANO_PIANO_0 (saved by Fritzing 0.9.3b)
breadboards: 1

parts:
  Part1 = Arduino Uno (Rev3)
  R2 = Resistor [tolerance=±5% resistance=220 package=THT]
  R1 = Resistor [tolerance=±5% resistance=220 package=THT]
  R3 = Resistor [tolerance=±5% resistance=220 package=THT]
  R4 = Resistor [tolerance=±5% resistance=220 package=THT]
  R5 = Resistor [tolerance=±5% resistance=220 package=THT]
  J1 = Piezo Speaker

nets:
  N1: Part1.D11_PWM/MOSI, J1.pin1
  N2: Part1.D2, R2.Pin_1, R1.Pin_1, R3.Pin_1, R4.Pin_1, R5.Pin_1
  N3: Part1.D3_PWM, R1.Pin_0
  N4: Part1.D4, R2.Pin_0
  N5: Part1.D5_PWM, R3.Pin_0
  N6: Part1.D6_PWM, R5.Pin_0
  N7: Part1.D7, R4.Pin_0
  N8: Part1.GND, J1.pin2

notes:
  paper d'alumini
