# Fritzing sketch id4454_ArduinoNanoWIZ820ioSketch_0 (saved by Fritzing 0.7.0b)
breadboards: 1

parts:
  Nano1 = Arduino Nano v2.3
  WIZ820io1 = WIZ820io [part_number=WIZ820io]

nets:
  N1: Nano1.RST, WIZ820io1.nRESET
  GND: Nano1.GND, WIZ820io1.GND
  N2: Nano1.D10, WIZ820io1.nSS
  N3: Nano1.D11, WIZ820io1.MOSI
  N4: Nano1.D12, WIZ820io1.MISO
  N5: Nano1.D13, WIZ820io1.SCLK
  3V3: Nano1.3V3, WIZ820io1.VIN

notes:
  Arduino Nano connection to WIZ820io Ethernet Module
