# Fritzing sketch id4455_Weather_Station_0 (saved by Fritzing 0.9.3b)
breadboards: 2

parts:
  Part1 = Arduino Mega 2560 (Rev3)
  Water_Level_Sensor1 = richardbruneau00000
  Water_Level_Sensor2 = richardbruneau00000
  Water_Level_Sensor3 = richardbruneau00000
  Water_Level_Sensor4 = richardbruneau00000
  Water_Level_Sensor5 = richardbruneau00000
  YL-83_-_Detection_Board1 = richardbruneau00000
  YL-83_-_Control_Board1 = richardbruneau00000
  DHT1 = DHT22_Humidity_and_Temperature_Sensor
  R1 = Resistor [tolerance=±5% resistance=10k package="0805 [SMD]"]
  J1 = 3.81mm Camdenboss Plug Socket - 3 [part_number=CTB93HE-3]
  U1 = NodeMCU
  J2 = 3.81mm Plugable Screw Terminal-PCB [part_number=CTB93HE-2]

nets:
  N1: Part1.A0, Water_Level_Sensor5.connector8
  N2: Part1.A1, Water_Level_Sensor2.connector8
  N3: Part1.A2, Water_Level_Sensor1.connector8
  N4: Part1.A3, Water_Level_Sensor3.connector8
  N5: Part1.A4, Water_Level_Sensor4.connector8
  N6: Part1.A5, J1.connector1
  N7: Part1.A6, J2.connector1
  N8: Part1.D19/RX1, U1.connector12
  N9: Part1.D18/TX1, U1.connector11
  N10: Part1.GND, Water_Level_Sensor1.connector10, Water_Level_Sensor2.connector10, Water_Level_Sensor3.connector10, Water_Level_Sensor4.connector10, Water_Level_Sensor5.connector10, YL-83_-_Control_Board1.connector9, DHT1.connector4, J1.connector0, U1.connector13
  N11: Part1.5V, Water_Level_Sensor1.connector9, Water_Level_Sensor2.connector9, Water_Level_Sensor3.connector9, Water_Level_Sensor4.connector9, Water_Level_Sensor5.connector9, YL-83_-_Control_Board1.connector8, DHT1.connector1, R1.Pin_1, J1.connector3, U1.connector15, J2.connector0
  N12: Part1.D51, DHT1.connector2, R1.Pin_0
  N13: Part1.D53, YL-83_-_Control_Board1.connector10
  N14: YL-83_-_Detection_Board1.connector8, YL-83_-_Control_Board1.connector12
  N15: YL-83_-_Detection_Board1.connector9, YL-83_-_Control_Board1.connector13
