# Fritzing sketch id4456_Warning_blink_5_led_2_0 (saved by Fritzing 0.9.3b)
circuit board: 8.46667cm x 5.64444cm
breadboards: 1

parts:
  Part1 = Arduino Uno (Rev3)
  LED1 = LED - 5mm [color="Red (633nm)" package="5 mm [THT]"]
  LED2 = LED - 5mm [color="Red (633nm)" package="5 mm [THT]"]
  LED3 = LED - 5mm [color="Red (633nm)" package="5 mm [THT]"]
  LED4 = LED - 5mm [color="Red (633nm)" package="5 mm [THT]"]
  LED5 = LED - 5mm [color="Red (633nm)" package="5 mm [THT]"]

nets:
  N1: Part1.D2, LED5.cathode
  N2: Part1.D3_PWM, LED4.cathode
  N3: Part1.D4, LED3.cathode
  N4: Part1.D5_PWM, LED2.cathode
  N5: Part1.D6_PWM, LED1.cathode
  N6: Part1.3V3, LED1.anode, LED2.anode, LED3.anode, LED4.anode, LED5.anode

notes:
  5 LED WARNING BLINK
