# Fritzing sketch id4457_Warning_blink_5_led_2_Esn730e_0 (saved by Fritzing 0.9.3b)
circuit board: 8.46667cm x 5.64444cm
breadboards: 1

parts:
  Part1 = Arduino Uno (Rev3)
  LED1 = LED - 5mm [color="Red (633nm)" package="5 mm [THT]"]
  LED2 = LED - 5mm [color="Red (633nm)" package="5 mm [THT]"]
  LED3 = LED - 5mm [color="Red (633nm)" package="5 mm [THT]"]
  LED4 = LED - 5mm [color="Red (633nm)" package="5 mm [THT]"]
  LED5 = LED - 5mm [color="Red (633nm)" package="5 mm [THT]"]

nets:
  N1: Part1.D2, LED5.cathode
  N2: Part1.D3_PWM, LED4.cathode
  N3: Part1.D4, LED3.cathode
  N4: Part1.D5_PWM, LED2.cathode
  N5: Part1.D6_PWM, LED1.cathode
  N6: Part1.3V3, LED1.anode, LED2.anode, LED3.anode, LED4.anode, LED5.anode

notes:
  // BLINK MODE 5 LED WARNING
  int led1 = 2;
  int led2 = 3;
  int led3 = 4;
  int led4 = 5;
  int led5 = 6;
  void setup() {
  pinMode(led1,OUTPUT);
  pinMode(led2,OUTPUT);
  pinMode(led3,OUTPUT);
  pinMode(led4,OUTPUT);
  pinMode(led5,OUTPUT);
  }
  void loop()
  {
  blink_1();
  blink_1();
  blink_1();
  blink_1();
  blink_2();
  blink_2();
  blink_2();
  blink_2();
  blink_3();
  blink_3();
  blink_4();
  blink_4();
  }
  void blink_1()
  {
  int t=100;
  digitalWrite(led1,HIGH);
  digitalWrite(led2,LOW);
  digitalWrite(led3,LOW);
  digitalWrite(led4,LOW);
  digitalWrite(led5,HIGH);
  delay(t);
  //----------------------
  digitalWrite(led1,LOW);
  digitalWrite(led2,HIGH);
  digitalWrite(led3,HIGH);
  digitalWrite(led4,HIGH);
  digitalWrite(led5,LOW);
  delay(t+100);
  }
  void blink_2()
  {
  int t=100;
  digitalWrite(led1,HIGH);
  digitalWrite(led2,HIGH);
  digitalWrite(led3,HIGH);
  digitalWrite(led4,LOW);
  digitalWrite(led5,LOW);
  delay(t);
  //--------------------
  digitalWrite(led1,LOW);
  digitalWrite(led2,LOW);
  digitalWrite(led3,HIGH);
  digitalWrite(led4,HIGH);
  digitalWrite(led5,HIGH);
  delay(t+100);
  }
  void blink_3()
  {
  int t=100;
  digitalWrite(led1,HIGH);
  delay(t);
  digitalWrite(led2,HIGH);
  delay(t);
  digitalWrite(led3,HIGH);
  delay(t);
  digitalWrite(led4,HIGH);
  delay(t);
  digitalWrite(led5,HIGH);
  delay(t);
  digitalWrite(led1,LOW);
  delay(t);
  digitalWrite(led2,LOW);
  delay(t);
  digitalWrite(led3,LOW);
  delay(t);
  digitalWrite(led4,LOW);
  delay(t);
  digitalWrite(led5,LOW);
  delay(t);
  digitalWrite(led5,HIGH);
  delay(t);
  digitalWrite(led4,HIGH);
  delay(t);
  digitalWrite(led3,HIGH);
  delay(t);
  digitalWrite(led2,HIGH);
  delay(t);
  digitalWrite(led1,HIGH);
  delay(t);
  //--------------------
  }
  void blink_4()
  {
  int t=100;
  digitalWrite(led1,LOW);
  delay(t);
  digitalWrite(led2,LOW);
  delay(t);
  digitalWrite(led3,LOW);
  delay(t);
  digitalWrite(led4,LOW);
  delay(t);
  digitalWrite(led5,LOW);
  delay(t);
  digitalWrite(led1,HIGH);
  delay(t);
  digitalWrite(led2,HIGH);
  delay(t);
  digitalWrite(led3,HIGH);
  delay(t);
  digitalWrite(led4,HIGH);
  delay(t);
  digitalWrite(led5,HIGH);
  delay(t);
  digitalWrite(led5,LOW);
  delay(t);
  digitalWrite(led4,LOW);
  delay(t);
  digitalWrite(led3,LOW);
  delay(t);
  digitalWrite(led2,LOW);
  delay(t);
  digitalWrite(led1,LOW);
  delay(t);
  }
