# Fritzing sketch id445_Arduino_crepuscolare_led_e_fotoresistenza_0 (saved by Fritzing 0.9.2b)
breadboards: 1

parts:
  LED1 = LED - 5mm [color="Red (633nm)" package="5 mm [THT]"]
  R1 = Photocell (LDR) [package=THT]
  Componente1 = Arduino Uno (Rev3)
  R2 = Resistor [tolerance=±5% resistance=220 package=THT]
  R3 = Resistor [tolerance=±5% resistance=10k package=THT]

nets:
  N1: LED1.cathode, R1.pin_1, Componente1.GND
  N2: LED1.anode, R2.Pin_0
  N3: R1.pin_0, Componente1.A0, R3.Pin_1
  N4: Componente1.D10_PWM/SS, R2.Pin_1
  N5: Componente1.5V, R3.Pin_0
