# Fritzing sketch id446_Untitled_Sketch_2_0 (saved by Fritzing 0.9.3b)
breadboards: 1

parts:
  Componente1 = Arduino Uno (Rev3)
  Componente2 = HC-06
  J1 = Basic Servo
  hc-sr1 = hc-sr04
  LED1 = smd LED [color="Red (633nm)" package="0603 [SMD]"]
  R1 = Resistor [tolerance=±5% resistance=220 package="2512 [SMD]"]
  e-radionica1 = prefix101209 [part_number=101209]

nets:
  N1: Componente1.D8, e-radionica1.connector7
  N2: Componente1.D12/MISO, R1.Pin_0
  GND: Componente1.GND, Componente2.connector14, J1.gnd, hc-sr1.GND, e-radionica1.connector1
  N3: Componente1.D0/RX, Componente2.connector13
  N4: Componente1.D1/TX, Componente2.connector12
  N5: Componente1.D2, e-radionica1.connector4
  N6: Componente1.D3_PWM, e-radionica1.connector3
  N7: Componente1.D4, e-radionica1.connector6
  N8: Componente1.D5_PWM, e-radionica1.connector5
  N9: Componente1.D6_PWM, hc-sr1.Echo
  VCC: Componente1.D7, Componente1.5V, Componente2.connector15, J1.vcc, hc-sr1.VCC, hc-sr1.Trig
  N10: Componente1.3V3, e-radionica1.connector8
  N11: LED1.cathode, R1.Pin_1
