# Fritzing sketch id4483_WaterFlowController_0 (saved by Fritzing 0.9.2b)
breadboards: 1

parts:
  L1 = Solenoid
  R1 = Resistor [tolerance=±5% resistance=1k package=THT]
  Matrix_keypad1 = CMG
  U1 = PCF8574 [package="DIP16 [THT]"]
  LCD2 = LCD screen
  R3 = Resistor [tolerance=±5% resistance=10k package=THT]
  D1 = Diode [package=diode-1n4001]
  Arduino2 = Arduino
  Q1 = npn-Powertransistor [package="TO220 [THT]"]

nets:
  N1: L1.pin1, Q1.collector
  VCC: L1.pin2, U1.VCC, LCD2.VDD, LCD2.LED+, D1.C
  N2: R1.Pin_0, Arduino2.D4
  N3: R1.Pin_1, Q1.base
  N4: Matrix_keypad1.connector25, U1.P7
  N5: Matrix_keypad1.connector26, U1.P6
  N6: Matrix_keypad1.connector27, U1.P5
  N7: Matrix_keypad1.connector28, U1.P4
  N8: Matrix_keypad1.connector29, U1.P3
  N9: Matrix_keypad1.connector30, U1.P2
  N10: Matrix_keypad1.connector31, U1.P1
  N11: Matrix_keypad1.connector32, U1.P0
  GND: U1.GND, LCD2.VSS, LCD2.V0, LCD2.R/W, LCD2.LED-, R3.Pin_0, Arduino2.GND, Q1.emitter
  N12: U1.SCL, Arduino2.A5
  N13: U1.SDA, Arduino2.A4
  N14: LCD2.RS, Arduino2.D7
  N15: LCD2.E, Arduino2.D8
  N16: LCD2.DB4, Arduino2.D9
  N17: LCD2.DB5, Arduino2.D10
  N18: LCD2.DB6, Arduino2.D11
  N19: LCD2.DB7, Arduino2.D12
  N20: R3.Pin_1, Arduino2.D2

notes:
  20x4 Line LCD Display
  To water flow sensor
  Black = Gnd
  Red = Vss
  Yellow = Signal
  Plastic Water Solenoid Valve – 12V – 1/2″
