# Fritzing sketch id4484_WaterControl_0 (saved by Fritzing 0.9.2b)
breadboards: 1

parts:
  Part1 = Arduino Mega 2560 (Rev3)
  DS3234_RTC = DeadOn RTC - DS3234 Breakout
  RGB_LED = RGB LED - (4 legs) [package="5 mm [THT]"]
  R4 = Resistor [tolerance=±5% resistance=330 package=THT]
  R2 = Resistor [tolerance=±5% resistance=330 package=THT]
  R3 = Resistor [tolerance=±5% resistance=330 package=THT]
  C1 = Electrolytic Capacitor [capacitance=4.7mF voltage=20V package="100 mil [THT, electrolytic]"]
  Water_Flow_Meter = HALL-EFFECT [package=sc70]
  12V_Supply = Power Jack [package=power_jack_slot]
  Nokia_5110_LCD = Nokia5110LCDModule
  Solenoid_in_Tap = Solenoid
  IC1 = Ywrobot_2_channel_relay
  U1 = TinySineGSMshield

nets (from the breadboard view):
  N1: Part1.D19/RX1, U1.connector1
  N2: Part1.D18/TX1, U1.connector4
  N3: Part1.D10_PWM, DS3234_RTC.SS
  3V3: Part1.3V3, DS3234_RTC.VCC, Nokia_5110_LCD.connector0
  5V: Part1.5V, Water_Flow_Meter.VCC, IC1.connector0
  GND: Part1.GND, DS3234_RTC.GND, Water_Flow_Meter.GND, Nokia_5110_LCD.connector1, IC1.connector10
  N4: Part1.D2_PWM, Water_Flow_Meter.OUT
  N5: Part1.D3_PWM, DS3234_RTC.INT/SQW
  N6: Part1.D6_PWM, IC1.connector1
  N7: Part1.D7_PWM, IC1.connector2
  N8: Part1.D23, Nokia_5110_LCD.connector3
  N9: Part1.D24, Nokia_5110_LCD.connector2
  N10: Part1.D25, Nokia_5110_LCD.connector4
  N11: Part1.D40, R2.Pin_1
  N12: Part1.D42, R3.Pin_1
  N13: Part1.D44, R4.Pin_1
  N14: Part1.D50, DS3234_RTC.MISO
  N15: Part1.D51, DS3234_RTC.MOSI, Nokia_5110_LCD.connector5
  N16: Part1.D52, DS3234_RTC.SCLK, Nokia_5110_LCD.connector6
  N17: RGB_LED.red_cathode, R2.Pin_0
  N18: RGB_LED.green_cathode, R3.Pin_0
  N19: RGB_LED.blue_cathode, R4.Pin_0
  N20: C1.+, 12V_Supply.GNDBREAK, IC1.connector6, IC1.connector9
  N21: 12V_Supply.GND, IC1.connector7, IC1.connector8
  N22: Solenoid_in_Tap.pin1, IC1.connector4
  N23: Solenoid_in_Tap.pin2, IC1.connector5
