# Fritzing sketch id4486_level_indicator_0 (saved by Fritzing 0.9.2b)
breadboards: 2

parts:
  IC1 = IC, DIP package, 28 pins [chip_label=ATmega8]
  U1 = Voltage Regulator - 5V [package="DPak [SMD]"]
  VCC1 = Battery block 9V
  DI1 = 7-Segment LED Display [package=THT]
  R1 = Resistor [tolerance=±5% resistance=470 package=THT]
  Q1 = NPN-Transistor [part_number=BC547 package="TO92 [THT]"]
  J1 = Piezo Speaker
  R2 = Resistor [tolerance=±5% resistance=470 package=THT]
  Q2 = NPN-Transistor [part_number=BC547 package="TO92 [THT]"]
  Q3 = NPN-Transistor [part_number=BC547 package="TO92 [THT]"]
  R3 = Resistor [tolerance=±5% resistance=180k package=THT]
  R4 = Resistor [tolerance=±5% resistance=100k package=THT]
  R5 = Resistor [tolerance=±5% resistance=100 package=THT]
  R6 = Resistor [tolerance=±5% resistance=180k package=THT]
  R7 = Resistor [tolerance=±5% resistance=100k package=THT]
  R8 = Resistor [tolerance=±5% resistance=100 package=THT]
  Q4 = NPN-Transistor [part_number=BC547 package="TO92 [THT]"]
  R9 = Resistor [tolerance=±5% resistance=180k package=THT]
  R10 = Resistor [tolerance=±5% resistance=100 package=THT]
  R11 = Resistor [tolerance=±5% resistance=100k package=THT]
  Q5 = NPN-Transistor [part_number=BC547 package="TO92 [THT]"]
  R12 = Resistor [tolerance=±5% resistance=100 package=THT]
  R13 = Resistor [tolerance=±5% resistance=180k package=THT]
  R14 = Resistor [tolerance=±5% resistance=100k package=THT]
  Q6 = NPN-Transistor [part_number=BC547 package="TO92 [THT]"]
  R15 = Resistor [tolerance=±5% resistance=100 package=THT]
  R16 = Resistor [tolerance=±5% resistance=180k package=THT]
  R17 = Resistor [tolerance=±5% resistance=100k package=THT]
  Q7 = NPN-Transistor [part_number=BC547 package="TO92 [THT]"]
  R18 = Resistor [tolerance=±5% resistance=100 package=THT]
  R19 = Resistor [tolerance=±5% resistance=180k package=THT]
  R20 = Resistor [tolerance=±5% resistance=100k package=THT]
  Q8 = NPN-Transistor [part_number=BC547 package="TO92 [THT]"]
  R21 = Resistor [tolerance=±5% resistance=100 package=THT]
  R22 = Resistor [tolerance=±5% resistance=180k package=THT]
  R23 = Resistor [tolerance=±5% resistance=100k package=THT]
  Q9 = NPN-Transistor [part_number=BC547 package="TO92 [THT]"]
  R24 = Resistor [tolerance=±5% resistance=100 package=THT]
  R25 = Resistor [tolerance=±5% resistance=180k package=THT]
  R26 = Resistor [tolerance=±5% resistance=100k package=THT]

nets:
  N1: IC1.pin2, DI1.cathodeC
  N2: IC1.pin3, DI1.cathodeA
  N3: IC1.pin4, DI1.cathodeE
  N4: IC1.pin5, DI1.cathodeDP
  N5: IC1.pin6, DI1.cathodeF
  N6: IC1.pin7, IC1.pin20, IC1.pin21, U1.output_voltage, R1.Pin_0, Q1.E, R4.Pin_0, R7.Pin_1, R11.Pin_0, R14.Pin_0, R17.Pin_0, R23.Pin_0, R26.Pin_1
  N7: IC1.pin8, IC1.pin22, U1.GND, VCC1.-, R2.Pin_1, Q2.C, Q3.C
  N8: IC1.pin9, Q5.E, R13.Pin_1
  N9: IC1.pin10, Q4.E, R9.Pin_1
  N10: IC1.pin11, DI1.cathodeD
  N11: IC1.pin12, DI1.cathodeB
  N12: IC1.pin13, DI1.cathodeG
  N13: IC1.pin14, Q3.E, R6.Pin_1
  N14: IC1.pin15, Q2.E, R3.Pin_1
  N15: IC1.pin16, Q9.E, R25.Pin_1
  N16: IC1.pin17, Q8.E, R22.Pin_1
  N17: IC1.pin18, Q7.E, R19.Pin_1
  N18: IC1.pin19, Q6.E, R16.Pin_1
  N19: IC1.pin23, Q1.B
  N20: U1.input_voltage, VCC1.+
  N21: DI1.commAnode#7, R1.Pin_1
  N22: Q1.C, J1.pin2
  N23: J1.pin1, R2.Pin_0
  N24: Q2.B, R5.Pin_0
  N25: Q3.B, R8.Pin_0
  N26: R3.Pin_0, R4.Pin_1
  N27: R6.Pin_0, R7.Pin_0
  N28: Q4.B, R10.Pin_0
  N29: R9.Pin_0, R11.Pin_1
  N30: Q5.B, R12.Pin_0
  N31: R13.Pin_0, R14.Pin_1
  N32: Q6.B, R15.Pin_0
  N33: R16.Pin_0, R17.Pin_1
  N34: Q7.B, R18.Pin_0
  N35: R19.Pin_0, R20.Pin_1
  N36: Q8.B, R21.Pin_0
  N37: R22.Pin_0, R23.Pin_1
  N38: Q9.B, R24.Pin_0
  N39: R25.Pin_0, R26.Pin_0

notes:
  8
  0
  7
  1
  2
  3
  4
  5
  6
