# Fritzing sketch id4487_Water_Level_Indicator_using_Transistors_0 (saved by Fritzing 0.9.3b)
breadboards: 1

parts:
  VCC = 4 x AAA Battery Mount
  LED1 = LED - 5mm [color="Red (633nm)" package="5 mm [THT]"]
  R1 = Resistor [tolerance=±5% resistance=1k package=THT]
  R4 = Resistor [tolerance=±5% resistance=10k package=THT]
  Q1 = NPN-Transistor [part_number=BC547 package="TO92 [THT]"]
  LED2 = LED - 5mm [color="Yellow (595nm)" package="5 mm [THT]"]
  Q2 = NPN-Transistor [part_number=BC547 package="TO92 [THT]"]
  R2 = Resistor [tolerance=±5% resistance=1k package=THT]
  R5 = Resistor [tolerance=±5% resistance=10k package=THT]
  LED3 = LED - 5mm [color="Green (570nm)" package="5 mm [THT]"]
  Q3 = NPN-Transistor [part_number=BC547 package="TO92 [THT]"]
  R3 = Resistor [tolerance=±5% resistance=1k package=THT]
  R6 = Resistor [tolerance=±5% resistance=10k package=THT]

nets:
  N1: VCC.-, Q1.E, Q2.E, Q3.E
  N2: VCC.+, LED1.anode, LED2.anode, LED3.anode
  N3: LED1.cathode, R1.Pin_0
  N4: R1.Pin_1, Q1.C
  N5: R4.Pin_1, Q1.B
  N6: LED2.cathode, R2.Pin_0
  N7: Q2.B, R5.Pin_1
  N8: Q2.C, R2.Pin_1
  N9: LED3.cathode, R3.Pin_0
  N10: Q3.B, R6.Pin_1
  N11: Q3.C, R3.Pin_1

notes:
  Probes: M1, M2, M3, M4
