# Fritzing sketch id4488_water_level_indicator_0 (saved by Fritzing 0.9.0b)
breadboards: 1

parts:
  R1 = Resistor [tolerance=±5% resistance=220 package=THT]
  LED1 = LED - 5mm [color="Red (633nm)" package="5 mm [THT]"]
  Q1 = NPN-Transistor [part_number=BC548C package="TO92 [THT]"]
  Q2 = NPN-Transistor [part_number=BC548C package="TO92 [THT]"]
  Q3 = NPN-Transistor [part_number=BC548C package="TO92 [THT]"]
  R2 = Resistor [tolerance=±5% resistance=220 package=THT]
  R3 = Resistor [tolerance=±5% resistance=220 package=THT]
  VCC1 = Battery
  VCC2 = Battery
  LED2 = LED - 5mm [color="Red (633nm)" package="5 mm [THT]"]
  LED3 = LED - 5mm [color="Red (633nm)" package="5 mm [THT]"]
  R4 = Resistor [tolerance=±5% resistance=220 package=THT]
  R5 = Resistor [tolerance=±5% resistance=220 package=THT]
  R6 = Resistor [tolerance=±5% resistance=220 package=THT]

nets:
  N1: R1.Pin_1, Q3.B
  N2: LED1.cathode, R4.Pin_0
  N3: LED1.anode, VCC1.+, LED2.anode, LED3.anode
  N4: Q1.E, Q2.E, Q3.E, VCC2.-
  N5: Q1.B, R3.Pin_1
  N6: Q1.C, R6.Pin_1
  N7: Q2.B, R2.Pin_1
  N8: Q2.C, R5.Pin_1
  N9: Q3.C, R4.Pin_1
  N10: VCC1.-, VCC2.+
  N11: LED2.cathode, R5.Pin_0
  N12: LED3.cathode, R6.Pin_0

notes:
  Water Tank
  Lowest point is A, then B, then C, then D is the highest one
  A : red wire
  B : green
  C : yellow
  D : black
  A, B, C, and D as Sensors are Copper Wires placed in the water tank ...
