# Fritzing sketch id4489_Plant_Watering_System_recover_0 (saved by Fritzing 0.9.2b)
circuit board: 8.46667cm x 5.64444cm
breadboards: 1

parts:
  Part1 = Arduino Uno (Rev3) - ICSP
  Part3 = Memoire 1.0 - SD card log shield
  DHT1 = DHT11_Temperature_and_Humitidy_Sensor [part_number=DHT11]
  VALVE1 = Plastic_Solenoid_Valve
  LED1 = LED - 5mm [color="Red (633nm)" package="5 mm [THT]"]
  Part4 = richardbruneau00000
  Part5 = richardbruneau00000
  Q2 = Basic FET N-Channel [package="TO220 [THT]"]
  D1 = Zener Diode [part_number=1N4732A breakdown_voltage=3.6V package="300 mil [THT]"]
  R1 = Resistor [tolerance=±5% resistance=220 package=THT]
  S1 = Pushbutton [package=THT]
  Part8 = adafruit [part_number=354]
  Part9 = adafruit [part_number=354]
  Part10 = adafruit [part_number=353]
  Part11 = adafruit [part_number=353]
  Part12 = adafruit [part_number=353]

nets:
  N1: Part1.A1, Part3.A_IN_1, Part4.connector8
  GND: Part1.GND, Part3.GND, DHT1.connector4, LED1.cathode, Part4.connector9, Q2.source, R1.Pin_0, Part8.connector2, Part12.connector2
  N2: Part1.D11_PWM/MOSI, Part3.DIG_11, DHT1.connector2
  N3: Part1.D12/MISO, Part3.DIG_12, R1.Pin_1, S1.leg0
  N4: Part1.D13/SCK, Part3.DIG_13, LED1.anode
  N5: Part1.D4, Part3.DIG_4, Q2.gate
  N6: Part1.D6_PWM, Part3.DIG_6, Part4.connector10
  VIN: Part1.VIN, Part3.VIN, DHT1.connector1, VALVE1.connector1, D1.cathode, S1.leg1, Part9.connector1, Part10.connector1
  N7: VALVE1.connector2, Q2.drain, D1.anode
  N8: Part4.connector12, Part5.connector8
  N9: Part4.connector13, Part5.connector9
  N10: Part8.connector1, Part9.connector2
  N11: Part10.connector2, Part11.connector1
  N12: Part11.connector2, Part12.connector1

notes:
  7.4V battery pack built with 2 x 3.7V, in series, to power Arduino.
  I used a USB battery back.
  12V battery pack built with 3 x 3.7V, in series, to drive the valve.
  I used a 12V lithium battery pack.
