# Fritzing sketch id4490_bomba_0 (saved by Fritzing 0.9.3b)
breadboards: 1

parts:
  Componente1 = Arduino Uno (Rev3) - ICSP
  U1 = RELAY [package=relay-g5q]
  Q1 = TRANSISTOR_NPN [package=to-92-ammo]
  R1 = Resistor [tolerance=±5% resistance=220 package=THT]
  S1 = Round Pushbutton
  BAT1 = BC9VPC [package=bc9vpc]  # not connected
  M1 = DC Motor
  D1 = Diode [package=diode-hv]

nets:
  N1: Componente1.D2, S1.leg0
  N2: Componente1.D3_PWM, R1.Pin_1
  N3: Componente1.5V, Q1.C
  N4: Componente1.GND, U1.NC, S1.leg1
  N5: U1.MAIN, Q1.E, D1.C
  N6: U1.COIL1, M1.pin_2
  N7: Q1.B, R1.Pin_0
