# Fritzing sketch id4492_Water_Tank_Level_Sensor_G1_0 (saved by Fritzing 0.9.2b)
breadboards: 1

parts:
  Part1 = Arduino Uno (Rev3)
  R1 = Rotary Potentiometer (Small) [maximum_resistance=100kΩ package=THT]
  S1 = Pushbutton [package="[THT]"]
  R2 = Resistor [tolerance=±5% resistance=220 package=THT]
  LCD1 = LCD screen
  Part2 = SRF05 Ultrasonic Rangefinder
  LED1 = LED - 5mm [color="Red (633nm)" package="5 mm [THT]"]
  R3 = Resistor [tolerance=±5% resistance=220 package=THT]

nets:
  N1: Part1.D8, Part2.connector9
  N2: Part1.D9_PWM, Part2.connector10
  N3: Part1.D13/SCK, LED1.anode
  GND: Part1.GND, S1.Pin_3, S1.Pin_4, LCD1.VSS, LCD1.V0, LCD1.R/W, LCD1.LED-, Part2.connector11, R3.Pin_0
  N4: Part1.D2, LCD1.DB7
  N5: Part1.D3_PWM, LCD1.DB6
  N6: Part1.D4, LCD1.DB5
  N7: Part1.D5_PWM, LCD1.DB4
  N8: Part1.RESET, S1.Pin_1, S1.Pin_2
  N9: R1.leg1, R2.Pin_1
  N10: R1.wiper, LCD1.LED+
  N11: R2.Pin_0, LCD1.VDD, Part2.connector8
  N12: LED1.cathode, R3.Pin_1
