# Fritzing sketch id4493_sonerie_wav_extended_v0.4betta_0 (saved by Fritzing 0.9.0b)
circuit board: 6.26498cm x 2.706cm
breadboards: 1

parts:
  U5 = POT [part_number=10k package=trim_pot]
  U3 = Voltage Regulator LM1117 [package=sot223]
  C6 = Ceramic Capacitor [capacitance=47nF package="1206 [SMD, multilayer]"]
  R1 = Resistor [tolerance=±5% resistance=10 package="1206 [SMD]"]
  J1 = Screw terminal - 2 pins [package=THT]
  J2 = Screw terminal - 2 pins [package=THT]
  R4 = Resistor [tolerance=±5% resistance=256k package="1206 [SMD]"]
  U6 = ATTINY45 [package=so]
  R3 = Resistor [tolerance=±5% resistance=4.7k package="1206 [SMD]"]
  C12 = Ceramic Capacitor [capacitance=10nF package="0805 [SMD, multilayer]"]
  C10 = Ceramic Capacitor [capacitance=100nF package="0805 [SMD, multilayer]"]
  IC1 = SO08 [chip_label=IC package=SO]
  J5 = female pin header, 2 pins [form="♀ (female)"]
  S2 = Pushbutton [package=THT]
  U8 = microSD Socket [package=usd-socket-pp]
  C3 = Electrolytic Capacitor [capacitance=47µF package="0605 [SMD, electrolytic]"]
  R2 = Resistor [tolerance=±5% resistance=1k package="1206 [SMD]"]
  C8 = Tantalum Capacitor [capacitance=10µF voltage=35V package="C 6032 [SMD, tantalum]"]
  C9 = Tantalum Capacitor [capacitance=100µF voltage=16V package="C 6032 [SMD, tantalum]"]
  C2 = Ceramic Capacitor [capacitance=100nF package="0805 [SMD, multilayer]"]
  C11 = Tantalum Capacitor [capacitance=20µF package="C 6032 [SMD, tantalum]"]
  C5 = Ceramic Capacitor [capacitance=1nF package="0805 [SMD, multilayer]"]
  C7 = Tantalum Capacitor [capacitance=100µF voltage=16V package="D 7343 [SMD, tantalum]"]
  C4 = Electrolytic Capacitor [capacitance=220µF voltage=16V package="0807 [SMD, electrolytic]"]
  C1 = Ceramic Capacitor [capacitance=100nF package="0805 [SMD, multilayer]"]

nets:
  N1: U5.S, IC1.2
  N2: U5.E, C9.-
  GND: U5.A, U3.ADJ, R1.Pin_0, J1.pin2, J2.pin2, U6.GND, C12.1, C10.0, IC1.4, S2.leg1, U8.GND, C3.-, C2.0, C11.-, C5.0, C4.-, C1.0
  vcc 3.3v: U3.OUT, U6.VCC, C10.1, U8.VCC, C3.+, C11.+, C1.1
  +5v/5V: U3.IN, J1.pin1, IC1.6, C2.1, C4.+
  N3: C6.0, R1.Pin_1
  N4: C6.1, IC1.5, C7.+
  N5: J2.pin1, C7.-
  N6: R4.Pin_0, U6.PB1(MISO)
  audio: R4.Pin_1, C12.0, R2.Pin_1, C9.+
  N7: U6.PB5(NRES), U8.DI
  N8: U6.PB3(ADC3), U8.CS
  N9: U6.PB4(ADC2), R2.Pin_0
  N10: U6.PB0(MOSI), R3.Pin_1, U8.DO
  N11: U6.PB2(SCK_ADC1), U8.SCK
  N12: R3.Pin_0, S2.leg0
  N13: IC1.1, C8.+
  N14: IC1.3, C5.1
  N15: IC1.8, J5.pin2
  N16: J5.pin1, C8.-

notes:
  technologica
  Wav Player Mono 16Bit
  LM386
  Attiny 85
