# Fritzing sketch id4494_WTR011_0 (saved by Fritzing 0.4.3b)
breadboards: 1

parts:
  pot = Big Potentiometer
  Power_plug1 = Power plug
  7805 = Voltage Regulator - 5V [package="TO220 [THT]"]
  4n28 = Optocoupler [package=THT]
  Atmega328 = atmega168 [package="DIP28 [THT]"]
  100u = Electrolytic Capacitor [package=THT]
  1uF = Electrolytic Capacitor [package=THT]
  100u_2 = Electrolytic Capacitor [package=THT]
  100nf = Ceramic Capacitor [package=THT]
  1n4001 = Rectifier Diode [package="300 mil [THT]"]
  jack = mono mini jack
  LED1 = Red LED - 5mm
  100uF = Electrolytic Capacitor [package=THT]
  2_2k = Resistor [resistance=220 package=THT]
  100nf_2 = Ceramic Capacitor [package=THT]
  hole1 = header hole
  100nf_3 = header hole
  hole1_2 = header hole
  hole1_3 = header hole
  hole1_4 = header hole
  hole1_5 = header hole
  hole1_6 = header hole
  hole1_7 = header hole
  hole1_8 = header hole
  hole1_9 = header hole
  hole1_10 = header hole
  hole1_11 = header hole
  hole1_12 = header hole
  hole1_13 = header hole
  hole1_14 = header hole
  Gieskes_WTR = DIN-5 jack (MIDI)
  G = header hole
  5v = header hole
  470 = header hole
  hole1_15 = header hole
  >| = header hole
  hole1_16 = header hole
  220 = header hole
  hole1_17 = header hole
  100k = header hole
  220_2 = header hole
  hole1_18 = header hole
  hole1_19 = header hole
  2_2k_2 = header hole
  3_3k = Resistor [resistance=220 package=THT]
  Switch1 = Pushbutton 12mm omron
  hole1_20 = header hole
  hole1_21 = header hole
  16mhz = header hole
  10k = header hole
  220_3 = header hole
  gnd = header hole
  hole1_22 = header hole
  hole1_23 = header hole
  hole1_24 = header hole
  hole1_25 = header hole

nets:
  N1: pot.connector2, Power_plug1.connector1, 7805.GND, 4n28.Pin_4, Atmega328.Pin_8, Atmega328.Pin_22, 100u.-, 100u_2.-, 1n4001.anode, jack.connector1, 100uF.-, 2_2k.Pin_1, 100nf_2.pin_0, hole1.connector0, G.connector0, hole1_15.connector0, Switch1.connector1, 16mhz.connector0, gnd.connector0, hole1_25.connector0
  N2: pot.connector3, Atmega328.Pin_27, hole1_12.connector0
  N3: pot.connector4, 7805.output_voltage, Atmega328.Pin_7, Atmega328.Pin_20, 100u_2.+, 100uF.+, 100nf_3.connector0, 5v.connector0, 3_3k.Pin_0, 10k.connector0
  N4: Power_plug1.connector0, 7805.input_voltage, 100u.+, 1n4001.cathode
  N5: 4n28.Pin_1, hole1_16.connector0, 220.connector0
  N6: 4n28.Pin_2, Gieskes_WTR.connector2, >|.connector0
  N7: 4n28.Pin_5, Atmega328.Pin_2, 3_3k.Pin_1, hole1_22.connector0
  N8: 4n28.Pin_6, 100k.connector0
  N9: Atmega328.Pin_1, 100nf.pin_0, 220_3.connector0
  N10: Atmega328.Pin_3, hole1_23.connector0
  N11: Atmega328.Pin_4, Atmega328.Pin_5, 220_2.connector0, Switch1.connector3
  N12: Atmega328.Pin_6, LED1.cathode
  N13: Atmega328.Pin_9, hole1_21.connector0
  N14: Atmega328.Pin_10, hole1_20.connector0
  N15: Atmega328.Pin_12, hole1_4.connector0
  N16: Atmega328.Pin_13, hole1_3.connector0
  N17: Atmega328.Pin_14, hole1_2.connector0
  N18: Atmega328.Pin_15, hole1_19.connector0
  N19: Atmega328.Pin_16, hole1_5.connector0
  N20: Atmega328.Pin_17, hole1_6.connector0
  N21: Atmega328.Pin_18, hole1_7.connector0
  N22: Atmega328.Pin_19, hole1_8.connector0
  N23: Atmega328.Pin_21, hole1_18.connector0
  N24: Atmega328.Pin_23, hole1_9.connector0
  N25: Atmega328.Pin_24, hole1_11.connector0
  N26: Atmega328.Pin_25, hole1_10.connector0
  N27: Atmega328.Pin_26, hole1_13.connector0
  N28: Atmega328.Pin_28, hole1_14.connector0
  N29: 1uF.-, jack.connector0
  N30: 1uF.+, 2_2k.Pin_0, 100nf_2.pin_1, 2_2k_2.connector0
  N31: 100nf.pin_1, hole1_24.connector0
  N32: LED1.anode, 470.connector0
  N33: Gieskes_WTR.connector4, hole1_17.connector0
