# Fritzing sketch id4495_Untitled_Sketch_1_0 (saved by Fritzing 0.9.3b)

parts:
  Part1 = Arduino Uno (Rev3)
  Part2 = Bluetooth HC-05 Macho
  SEN1 = Pulse_Sensor
  Part3 = Triple Axis Accelerometer Breakout - ADXL345
  RHT2 = Humidity and Temperature Sensor RHT03
  S1 = SWITCH-MOMENTARY-2 [package=tactile_switch_smd-2]
  U2 = ESP8266_module [part_number=ESP8266]

nets:
  N1: Part1.A0, Part1.N/C, SEN1.connector2
  N2: Part1.A1, Part3.SDA, Part3.SCL
  N3: Part1.A2, Part3.SDO
  N4: Part1.A3, Part3.INT2
  N5: Part1.A4/SDA, RHT2.GND_1
  N6: Part1.A5/SCL, RHT2.Data-signal
  N7: Part1.D9_PWM, U2.connector1
  N8: Part1.D10_PWM/SS, U2.connector3
  N9: Part1.D11_PWM/MOSI, U2.connector5
  N10: Part1.D12/MISO, U2.connector7
  N11: Part1.D0/RX, Part2.TXD
  N12: Part1.D1/TX, Part2.RXD
  N13: Part1.3V3, S1.1
  N14: Part1.5V, S1.2

notes:
  Pulse Rate Sensor
  SN-1175
  Wi-Fi ESP8266
  Module
  Panic Button
  ADXL-335 Accelrometer
  DHT-11 Temperature and Humidity Sensor
  HC-05 Bluetooth Module
  Arduino Uno Microcontroller
