# Fritzing sketch id4496_Weather_Clock_0 (saved by Fritzing 0.9.0b)
circuit board: 8.46667cm x 5.64444cm
breadboards: 2

parts:
  LCM1602_IIC1 = generic_ic_dip_22_300mil.fzp [part_number="LCM1602 IIC" chip_label="LCM1602 IIC"]
  Componente1 = Arduino Uno (Rev3)
  Componente2 = Real Time Clock Module - DS1307 RTC Breakout Board
  LCD1_20x5 = lcd-GDM1602K.fzp
  RHT1 = Humidity and Temperature Sensor RHT03
  R1 = PHOTOCELL [package=photocell-kit]
  R2 = Resistor [tolerance=±5% resistance=330 package=THT]
  LED1 = LED - 5mm [color="Red (633nm)" package="5 mm [THT]"]
  U1 = SWITCH-SPST-2 [package=switch-spst-vertical]
  Componente4 = Barometric Pressure Sensor - BMP180 Breakout (GY-68)
  R4 = Resistor [tolerance=±5% resistance=10k package=THT]
  R5 = Resistor [tolerance=±5% resistance=10k package=THT]
  R6 = Resistor [tolerance=±5% resistance=10k package=THT]
  S5 = Pushbutton [package="[THT]"]
  S6 = Pushbutton [package="[THT]"]
  S7 = Pushbutton [package="[THT]"]
  Componente5 = Arduino Uno (Rev3)  # not connected
  R7 = Resistor [tolerance=±5% resistance=10k package=THT]
  R8 = Resistor [tolerance=±5% resistance=10k package=THT]
  R9 = Resistor [tolerance=±5% resistance=10k package=THT]
  S8 = Pushbutton [package="[THT]"]
  S9 = Pushbutton [package="[THT]"]
  S10 = Pushbutton [package="[THT]"]
  RHT2 = Humidity and Temperature Sensor RHT03
  Componente6 = Real Time Clock Module - DS1307 RTC Breakout Board
  Componente7 = Barometric Pressure Sensor - BMP180 Breakout (GY-68)
  LCM1602_IIC3 = generic_ic_dip_22_300mil.fzp [part_number="LCM1602 IIC" chip_label="LCM1602 IIC"]
  U2 = LCD-16X2 [package=lcd-16x2]  # not connected

nets:
  N1: LCM1602_IIC1.connector0, LCD1_20x5.connector0
  N2: LCM1602_IIC1.connector1, LCD1_20x5.connector1
  N3: LCM1602_IIC1.connector2, LCD1_20x5.connector2
  N4: LCM1602_IIC1.connector3, LCD1_20x5.connector3
  N5: LCM1602_IIC1.connector4, LCD1_20x5.connector4
  N6: LCM1602_IIC1.connector5, LCD1_20x5.connector5
  N7: LCM1602_IIC1.connector6, LCD1_20x5.connector6
  N8: LCM1602_IIC1.connector7, LCD1_20x5.connector7
  N9: LCM1602_IIC1.connector8, LCD1_20x5.connector8
  N10: LCM1602_IIC1.connector9, LCD1_20x5.connector9
  N11: LCM1602_IIC1.connector10, LCD1_20x5.connector10
  N12: LCM1602_IIC1.connector11, LCD1_20x5.connector11
  N13: LCM1602_IIC1.connector12, LCD1_20x5.connector12
  N14: LCM1602_IIC1.connector13, LCD1_20x5.connector13
  N15: LCM1602_IIC1.connector14, LCD1_20x5.connector14
  N16: LCM1602_IIC1.connector15, LCD1_20x5.connector15
  GND: LCM1602_IIC1.connector16, Componente1.GND, Componente2.GND, RHT1.GND_2, LED1.cathode, Componente4.GND, R4.Pin_0, R5.Pin_0, R6.Pin_0
  5V: LCM1602_IIC1.connector17, Componente1.5V, Componente2.5V, RHT1.Vcc, U1.O, Componente4.VCC, S5.Pin_1, S5.Pin_2, S6.Pin_1, S6.Pin_2, S7.Pin_1, S7.Pin_2
  N17: LCM1602_IIC1.connector18, Componente1.A5/SCL, Componente2.SDA, Componente4.SDA
  N18: LCM1602_IIC1.connector19, Componente1.A4/SDA, Componente2.SCL, Componente4.SCL
  N19: LCM1602_IIC1.connector20, R1.P$2
  N20: LCM1602_IIC1.connector21, R1.P$1
  N21: Componente1.D8, RHT1.Data-signal
  N22: Componente1.D13/SCK, R2.Pin_0
  N23: R2.Pin_1, LED1.anode
  N24: R4.Pin_1, S5.Pin_3, S5.Pin_4
  N25: R5.Pin_1, S6.Pin_3, S6.Pin_4
  N26: R6.Pin_1, S7.Pin_3, S7.Pin_4
  GND_2: R7.Pin_0, R8.Pin_0, R9.Pin_0, RHT2.GND_2, Componente6.GND, Componente7.GND, LCM1602_IIC3.connector16
  N27: R7.Pin_1, S8.Pin_3, S8.Pin_4
  N28: R8.Pin_1, S9.Pin_3, S9.Pin_4
  N29: R9.Pin_1, S10.Pin_3, S10.Pin_4
  VCC: S8.Pin_1, S8.Pin_2, S9.Pin_1, S9.Pin_2, S10.Pin_1, S10.Pin_2, RHT2.Vcc, Componente6.5V, Componente7.VCC, LCM1602_IIC3.connector17
  N30: Componente6.SCL, Componente7.SCL, LCM1602_IIC3.connector19
  N31: Componente6.SDA, Componente7.SDA, LCM1602_IIC3.connector18
