# Fritzing sketch id4497_Weather_Clock2_0 (saved by Fritzing 0.9.0b)
breadboards: 1

parts:
  Componente5 = Arduino Uno (Rev3)
  RHT2 = Humidity and Temperature Sensor RHT03
  Componente6 = Real Time Clock Module - DS1307 RTC Breakout Board
  Componente7 = Barometric Pressure Sensor - BMP180 Breakout (GY-68)
  LCM1602_IIC3 = generic_ic_dip_22_300mil.fzp [part_number="LCM1602 IIC" chip_label="LCM1602 IIC"]
  U2 = LCD-16X2 [package=lcd-16x2]
  S11 = Pushbutton [package="[THT]"]
  S12 = Pushbutton [package="[THT]"]
  S13 = Pushbutton [package="[THT]"]
  R14 = Resistor [tolerance=±5% resistance=10k package=THT]
  R15 = Resistor [tolerance=±5% resistance=10k package=THT]
  R16 = Resistor [tolerance=±5% resistance=10k package=THT]
  LED2 = LED - 5mm [color="Red (633nm)" package="5 mm [THT]"]
  R17 = Resistor [tolerance=±5% resistance=1k package=THT]
  R18 = Resistor [tolerance=±5% resistance=330 package=THT]
  PIR1 = PIR_sensor
  R19 = Photocell (LDR) [package=THT]

nets:
  N1: Componente5.A4/SDA, Componente6.SDA, Componente7.SDA, LCM1602_IIC3.connector18
  N2: Componente5.A5/SCL, Componente6.SCL, Componente7.SCL, LCM1602_IIC3.connector19
  N3: Componente5.D8, S13.Pin_3, S13.Pin_4, R15.Pin_1
  N4: Componente5.D13/SCK, LED2.anode
  GND: Componente5.GND, RHT2.GND_2, Componente6.GND, Componente7.GND, LCM1602_IIC3.connector16, R14.Pin_0, R15.Pin_0, R16.Pin_0, R18.Pin_0, PIR1.connector3
  N5: Componente5.D2, PIR1.connector2
  N6: Componente5.D6_PWM, S11.Pin_3, S11.Pin_4, R16.Pin_1
  N7: Componente5.D7, S12.Pin_3, S12.Pin_4, R14.Pin_1
  5V: Componente5.5V, RHT2.Vcc, Componente6.5V, Componente7.VCC, LCM1602_IIC3.connector17, S11.Pin_1, S11.Pin_2, S12.Pin_1, S12.Pin_2, S13.Pin_1, S13.Pin_2, R17.Pin_0, PIR1.connector1
  N8: RHT2.Data-signal, RHT2.GND_1, R17.Pin_1
  N9: LCM1602_IIC3.connector0, U2.VSS
  N10: LCM1602_IIC3.connector1, U2.VDD
  N11: LCM1602_IIC3.connector2, U2.VO
  N12: LCM1602_IIC3.connector3, U2.RS
  N13: LCM1602_IIC3.connector4, U2.R_W
  N14: LCM1602_IIC3.connector5, U2.E
  N15: LCM1602_IIC3.connector6, U2.DB0
  N16: LCM1602_IIC3.connector7, U2.DB1
  N17: LCM1602_IIC3.connector8, U2.DB2
  N18: LCM1602_IIC3.connector9, U2.DB3
  N19: LCM1602_IIC3.connector10, U2.DB4
  N20: LCM1602_IIC3.connector11, U2.DB5
  N21: LCM1602_IIC3.connector12, U2.DB6
  N22: LCM1602_IIC3.connector13, U2.DB7
  N23: LCM1602_IIC3.connector14, U2.A
  N24: LCM1602_IIC3.connector15, U2.K
  N25: LCM1602_IIC3.connector20, R19.pin_1
  N26: LCM1602_IIC3.connector21, R19.pin_0
  N27: LED2.cathode, R18.Pin_1
