# Fritzing sketch id449_Dimmer_RGB_0 (saved by Fritzing 0.9.2b)
breadboards: 1

parts:
  LED1 = RGB LED (com. cathode, rbg) [package="5 mm [THT]"]
  R1 = Resistor [tolerance=±5% resistance=220 package="2512 [SMD]"]
  R2 = Resistor [tolerance=±5% resistance=220 package="2512 [SMD]"]
  R3 = Resistor [tolerance=±5% resistance=220 package="2512 [SMD]"]
  Componente1 = Arduino Uno (Rev3)
  S1 = Momentary Switch [package=ksa_sealed_tac_switch]
  S2 = Momentary Switch [package=ksa_sealed_tac_switch]
  R4 = Resistor [tolerance=±5% resistance=10k package="0805 [SMD]"]
  R5 = Resistor [tolerance=±5% resistance=10k package="0805 [SMD]"]
  R6 = Resistor [tolerance=±5% resistance=220 package="2512 [SMD]"]
  U2 = 7-SEGMENT-DISPLAY [package=7-segment-display]
  U3 = 74HC595 [package="DIP16 [THT]"]

nets:
  N1: LED1.red_anode, R3.Pin_0
  5V: LED1.common_cathode, Componente1.5V, S1.3, S2.3, R6.Pin_0, U3.MR, U3.VCC
  N2: LED1.blue_anode, R2.Pin_0
  N3: LED1.green_anode, R1.Pin_0
  N4: R1.Pin_1, Componente1.D3_PWM
  N5: R2.Pin_1, Componente1.D5_PWM
  N6: R3.Pin_1, Componente1.D9_PWM
  N7: Componente1.D10_PWM/SS, Componente1.D11_PWM/MOSI, U3.ST_CP
  N8: Componente1.D2, U3.DS
  N9: Componente1.D6_PWM, S1.2
  N10: Componente1.D7, S2.2
  GND: Componente1.GND, R4.Pin_0, R5.Pin_0, U3.GND, U3.OE
  N11: S1.1, R4.Pin_1
  N12: S2.1, R5.Pin_1
  N13: R6.Pin_1, U2.G2
  N14: U2.E, U3.Q5
  N15: U2.D, U3.Q4
  N16: U2.C, U3.Q3
  N17: U2.DP, U3.Q0
  N18: U2.B, U3.Q2
  N19: U2.A, U3.Q1
  N20: U2.F, U3.Q6
  N21: U2.G, U3.Q7

notes:
  RGB catodo com.
  ©Alessandro Oss
