# Fritzing sketch id449_Kitchen_Timer (saved by Fritzing 0.4.3b)
breadboards: 1

parts:
  Arduino1 = Arduino
  S1 = Pushbutton [package="[THT]"]
  R1 = Resistor [resistance=10k package=THT]
  LED1 = Red LED - 5mm
  LED2 = Red LED - 5mm
  LED3 = Red LED - 5mm
  LED4 = Red LED - 5mm
  LED5 = Red LED - 5mm
  LED6 = Red LED - 5mm
  LED7 = Red LED - 5mm
  LED8 = Red LED - 5mm
  LED9 = Red LED - 5mm
  LED10 = Red LED - 5mm
  J1 = Piezo Speaker

nets:
  N1: Arduino1.GND, R1.Pin_1, LED1.cathode, LED2.cathode, LED3.cathode, LED4.cathode, LED5.cathode, LED6.cathode, LED7.cathode, LED8.cathode, LED9.cathode, LED10.cathode, J1.pin1
  N2: Arduino1.D13, LED10.anode
  N3: Arduino1.D12, LED9.anode
  N4: Arduino1.D11, LED8.anode
  N5: Arduino1.D10, LED1.anode
  N6: Arduino1.D9, LED2.anode
  N7: Arduino1.D8, J1.pin2
  N8: Arduino1.D7, LED3.anode
  N9: Arduino1.D6, LED4.anode
  N10: Arduino1.D5, LED5.anode
  N11: Arduino1.D4, LED6.anode
  N12: Arduino1.D3, LED7.anode
  N13: Arduino1.D2, S1.Pin_1, S1.Pin_2, R1.Pin_0
  N14: Arduino1.+5V, S1.Pin_3, S1.Pin_4

notes:
  These LED's are actually an LED bar graph display, but I cannot make that on Fritzing
