# Fritzing sketch id4500_Weersafhankelijke_regeling_8C_0 (saved by Fritzing 0.9.1b)
circuit board: 4.40457cm x 5.3166cm
breadboards: 1

parts:
  R2 = Resistor [tolerance=±5% resistance=4.7k package=THT]
  Q1 = NPN-Transistor [package="TO92 [THT]"]
  J1 = male pin header, 8 pins [form="♂ (male)"]
  J2 = male pin header, 8 pins [form="♂ (male)"]
  J3 = male pin header, 6 pins [form="♂ (male)"]
  J4 = male pin header, 6 pins [form="♂ (male)"]
  C2 = Ceramic Capacitor [capacitance=100nF package="100 mil [THT, multilayer]"]
  C1 = Ceramic Capacitor [capacitance=100nF package="100 mil [THT, multilayer]"]
  D1 = Rectifier Diode [part_number=1N4001 package="300 mil [THT]"]
  R3 = Resistor [tolerance=±5% resistance=220 package=THT]
  R4 = Resistor [tolerance=±5% resistance=220 package=THT]
  R5 = Resistor [tolerance=±5% resistance=220 package=THT]
  LED1 = LED - 5mm [color="Red (633nm)" package="5 mm [THT]"]
  LED3 = LED - 5mm [color="Red (633nm)" package="5 mm [THT]"]
  LED2 = LED - 5mm [color="Red (633nm)" package="5 mm [THT]"]
  LED4 = LED - 5mm [color="Red (633nm)" package="5 mm [THT]"]
  R6 = Resistor [tolerance=±5% resistance=220 package=THT]
  S1 = screw terminal, 3 pins
  S2 = screw terminal, 3 pins
  Rel1 = female pin header, 4 pins [form="♀ (female)"]
  P1 = screw terminal, 3 pins
  P2 = screw terminal, 3 pins
  S3 = screw terminal, 2 pins
  S4 = screw terminal, 2 pins
  R1 = Resistor [tolerance=±5% resistance=4.7k package=THT]
  C3 = Ceramic Capacitor [capacitance=100nF package="100 mil [THT, multilayer]"]
  P3 = screw terminal, 3 pins

nets:
  N1: R2.Pin_0, Q1.B
  N2: R2.Pin_1, J1.pin8
  GND: Q1.E, J3.pin5, C2.1, C1.1, LED1.cathode, LED3.cathode, LED2.cathode, S1.pin1, S2.pin1, P1.pin1, P2.pin1, C3.0, P3.pin1
  N3: Q1.C, D1.anode, R6.Pin_1, Rel1.pin3
  N4: J2.pin1, R3.Pin_1
  N5: J2.pin2, R4.Pin_1
  N6: J2.pin3, R5.Pin_1
  N7: J2.pin6, S1.pin2, S2.pin2, R1.Pin_1
  5V: J3.pin3, C2.0, C1.0, D1.cathode, LED4.anode, S1.pin3, S2.pin3, Rel1.pin2, P1.pin3, P2.pin3, R1.Pin_0, C3.1, P3.pin3
  N8: J4.pin1, P1.pin2
  N9: J4.pin2, P2.pin2
  N10: J4.pin3, P3.pin2
  N11: R3.Pin_0, LED1.anode
  N12: R4.Pin_0, LED2.anode
  N13: R5.Pin_0, LED3.anode
  N14: LED4.cathode, R6.Pin_0
  N15: Rel1.pin1, S4.pin1
  N16: Rel1.pin4, S3.pin2
  N17: S3.pin1, S4.pin2

notes:
  RT/ABB
  WAR_8C
  +
  -
  d
