# Fritzing sketch id4502_weather_station_0 (saved by Fritzing 0.9.1b)
breadboards: 1

parts:
  LCD1 = LCD screen
  Part1 = Arduino Nano (Rev3.0)
  Ethernet_board1 = ENC28J60_Ethernet_breakoutboard_variant1_v9
  Part2 = Real Time Clock Module - DS1307 RTC Breakout Board
  DHT1 = DHT22_Humidity_and_Temperature_Sensor

nets:
  GND: LCD1.VSS, LCD1.V0, LCD1.R/W, LCD1.LED-, Part1.GND, Ethernet_board1.connector10, Part2.GND, DHT1.connector4
  N1: LCD1.VDD, LCD1.LED+, Ethernet_board1.connector9, DHT1.connector1
  N2: LCD1.RS, Part1.D7
  N3: LCD1.E, Part1.D6
  N4: LCD1.DB4, Part1.D5
  N5: LCD1.DB5, Part1.D4
  N6: LCD1.DB6, Part1.D3
  N7: LCD1.DB7, Part1.D2
  N8: Part1.RESET, Ethernet_board1.connector8
  N9: Part1.D8, DHT1.connector2
  N10: Part1.D10, Ethernet_board1.connector7
  N11: Part1.D11/MOSI, Ethernet_board1.connector5
  N12: Part1.D12/MISO, Ethernet_board1.connector4
  5V: Part1.5V, Part2.5V
  N13: Part1.A5, Part2.SCL
  N14: Part1.A4, Part2.SDA
  N15: Part1.D13/SCK, Ethernet_board1.connector6
