# Fritzing sketch id4505_weather_0 (saved by Fritzing 0.9.2b)
circuit board: 4.79585cm x 5.83023cm
breadboards: 1

parts:
  BMP280 = male pin header, 7 pins [form="♂ (male)"]
  Nano = Arduino Nano (Rev3.0)
  OLED = female pin header, 4 pins [form="♀ (female)"]
  R1 = Resistor [tolerance=±5% resistance=4.7k package=THT]
  R2 = Resistor [tolerance=±5% resistance=4.7k package=THT]
  RF_IN = female pin header, 4 pins [form="♀ (female)"]
  DC_IN = Power Jack [package=power_jack_slot]

nets:
  N1: BMP280.pin1, Nano.5V, OLED.pin2, R1.Pin_1, R2.Pin_1, RF_IN.pin4
  GND: BMP280.pin3, Nano.GND, OLED.pin1, RF_IN.pin1, DC_IN.GND
  N2: BMP280.pin4, Nano.D13/SCK
  N3: BMP280.pin5, Nano.D12/MISO
  N4: BMP280.pin6, Nano.D11/MOSI
  N5: BMP280.pin7, Nano.D10
  N6: Nano.D2, RF_IN.pin3
  N7: Nano.VIN, DC_IN.PWR
  N8: Nano.A5, OLED.pin3, R1.Pin_0
  N9: Nano.A4, OLED.pin4, R2.Pin_0

notes:
  Mk1
  433Mhz Rcv
  BMP280
  R1
  R2
