# Fritzing sketch id4506_Meteo_0 (saved by Fritzing 0.9.0b)
breadboards: 1

parts:
  U1 = ESP8266_module [part_number=ESP8266]
  R1 = Resistor [tolerance=±5% resistance=270 package=THT]
  C1 = Ceramic Capacitor [capacitance=100nF voltage=16V package="100 mil [THT, multilayer]"]
  C2 = Electrolytic Capacitor [capacitance=47µF voltage=16V package="100 mil [THT, electrolytic]"]
  R2 = Resistor [tolerance=±5% resistance=510 package=THT]
  R3 = Resistor [tolerance=±5% resistance=220 package=THT]
  R4 = Resistor [tolerance=±5% resistance=370 package=THT]
  R5 = Resistor [tolerance=±5% resistance=1k package=THT]
  U2 = LM317
  Componente1 = Barometric Pressure Sensor - BMP180 Breakout (GY-68)  # not connected
  RHT1 = Humidity and Temperature Sensor RHT03
  Componente2 = Arduino Uno (Rev3)
  Power_plug1 = Power plug

nets:
  N1: U1.connector0, U1.connector2, U1.connector4, R1.Pin_1
  N2: U1.connector1, U1.connector3, U1.connector5, R3.Pin_1, U2.connector1
  GND: U1.connector6, C1.0, C2.-, R2.Pin_0, R4.Pin_0, RHT1.GND_2, Componente2.GND, Power_plug1.GND
  N3: U1.connector7, Componente2.D2
  N4: R1.Pin_0, R2.Pin_1, Componente2.D3_PWM
  VCC: C1.1, C2.+, R5.Pin_0, U2.connector2, RHT1.Vcc, Componente2.5V, Power_plug1.VCC
  N5: R3.Pin_0, R4.Pin_1, U2.connector0
  N6: R5.Pin_1, RHT1.Data-signal, Componente2.D8
