# Fritzing sketch id4507_weather_station_0 (saved by Fritzing 0.9.2b)
breadboards: 1

parts:
  BMP180 = adafruit
  DHT11 = Humidity and Temperature Sensor RHT03
  Arduino_UNO = Arduino Uno (Rev3)
  R1 = Resistor [tolerance=±5% resistance=220 package=THT]
  R2 = Resistor [tolerance=±5% resistance=220 package=THT]
  LED = LED - 5mm [color="Green (555nm)" package="5 mm [THT]"]

nets:
  N1: BMP180.connector5, Arduino_UNO.ioref, Arduino_UNO.3V3
  N2: BMP180.connector6, DHT11.GND_2, Arduino_UNO.GND, R2.Pin_1
  N3: BMP180.connector7, Arduino_UNO.A5/SCL
  N4: BMP180.connector8, Arduino_UNO.A4/SDA
  VCC: DHT11.Vcc, Arduino_UNO.5V, R1.Pin_0
  N5: DHT11.Data-signal, Arduino_UNO.D8, R1.Pin_1
  N6: Arduino_UNO.D7, LED.anode
  N7: R2.Pin_0, LED.cathode
