# Fritzing sketch id4508_Survillance_Robot_0 (saved by Fritzing 0.9.2b)

parts:
  IC1 = L293D [package=THT]
  Part1 = JeePlug experimenter's board
  Raspberry_Pi1 = Raspberry Pi 2
  M1 = DC Motor
  M2 = DC Motor

nets:
  N1: IC1.Enable_1, IC1.+Vmotor, IC1.Enable_2, IC1.+V, Part1.N$7, Part1.N$21, Part1.N$39, Part1.N$45, Part1.N$47, Part1.N$53, Part1.N$55, Part1.N$57, Raspberry_Pi1.5V
  N2: IC1.In_1, Part1.N$10, Part1.N$16, Raspberry_Pi1.GPIO25
  N3: IC1.Out_1_(_Controlled_by_Enable_1_), Part1.N$11, Part1.N$17, M2.pin_2
  N4: IC1.0V, Part1.N$12, Part1.N$18, Part1.N$19, Part1.N$42, Part1.N$43, Part1.N$50, Raspberry_Pi1.GND
  N5: IC1.Out_2_(_Controlled_by_Enable_1_), Part1.N$14, Part1.N$20, M2.pin_1
  N6: IC1.In_2, Part1.N$15, Part1.N$22, Raspberry_Pi1.GPIO24
  N7: IC1.In_3, Part1.N$46, Part1.N$54, Raspberry_Pi1.GPIO23
  N8: IC1.Out_3_(_Controlled_by_Enable_2_), Part1.N$44, Part1.N$52, M1.pin_2
  N9: IC1.Out_4_(_Controlled_by_Enable_2_), Part1.N$41, Part1.N$49, M1.pin_1
  N10: IC1.In_4, Part1.N$40, Part1.N$48, Raspberry_Pi1.GPIO18
