# Fritzing sketch id450_temp_knock_lcd_0 (saved by Fritzing 0.9.2b)
breadboards: 1

parts:
  Part1 = Arduino Uno (Rev3)
  LCD1 = LCD screen
  R1 = Resistor [tolerance=±5% resistance=220 package=THT]
  T1 = TMP36 Temperature Sensor [package="TO92 [THT]"]
  J1 = Piezo Speaker
  R2 = Resistor [tolerance=±5% resistance=1M package=THT]

nets:
  N1: Part1.A0, T1.Vout
  N2: Part1.A1, J1.pin1, R2.Pin_0
  N3: Part1.D11_PWM/MOSI, LCD1.E
  N4: Part1.D12/MISO, LCD1.RS
  N5: Part1.D2, LCD1.DB7
  N6: Part1.D3_PWM, LCD1.DB6
  N7: Part1.D4, LCD1.DB5
  N8: Part1.D5_PWM, LCD1.DB4
  5V: Part1.5V, LCD1.VDD, R1.Pin_1, T1.+Vs, J1.pin2
  GND: Part1.GND, LCD1.VSS, LCD1.V0, LCD1.R/W, LCD1.LED-, T1.GND, R2.Pin_1
  N9: LCD1.LED+, R1.Pin_0
