# Fritzing sketch id4511_wechselblinker_v12a_0 (saved by Fritzing 0.9.0b)
circuit board: 4cm x 4cm
breadboards: 1

parts:
  T1_547 = NPN-Transistor [package="TO92 [THT]"]
  T2_547 = NPN-Transistor [package="TO92 [THT]"]
  C2 = Electrolytic Capacitor [capacitance=47µF package="100 mil [THT, electrolytic]"]
  R2 = Resistor [tolerance=±5% resistance=4.7k package=THT]
  R4 = Resistor [tolerance=±5% resistance=470 package=THT]
  L2 = LED - 5mm [color="Red (633nm)" package="5 mm [THT]"]
  L1 = LED - 5mm [color="Red (633nm)" package="5 mm [THT]"]
  R1 = Resistor [tolerance=±5% resistance=470 package=THT]
  C1 = Electrolytic Capacitor [capacitance=47µF package="100 mil [THT, electrolytic]"]
  R3 = Resistor [tolerance=±5% resistance=4.7k package=THT]
  P1 = Trimmer Potentiometer [maximum_resistance=100kΩ package=THT]
  VCC = Battery block 9V

nets:
  N1: T1_547.E, T2_547.E, VCC.-
  N2: T1_547.B, C2.-, R2.Pin_0
  N3: T1_547.C, R1.Pin_0, C1.+
  N4: T2_547.B, C1.-, R3.Pin_0
  N5: T2_547.C, C2.+, R4.Pin_0
  N6: R2.Pin_1, R3.Pin_1, P1.wiper
  N7: R4.Pin_1, L2.cathode
  N8: L2.anode, L1.anode, P1.leg2, VCC.+
  N9: L1.cathode, R1.Pin_1

notes:
  WECHSELBLINKER
