# Fritzing sketch id4512_Untitled_Sketch_0 (saved by Fritzing 0.9.3b)
circuit board: 8.46667cm x 5.64444cm
breadboards: 1

parts:
  VCC4 = Battery
  U1 = RELAY [package=relay-t9a-2]
  Q1 = PNP-Transistor [package="SOT-23 [SMD]"]
  Q2 = PNP-Transistor [package="SOT-23 [SMD]"]
  Q3 = PNP-Transistor [package="SOT-23 [SMD]"]
  Q4 = PNP-Transistor [package="SOT-23 [SMD]"]
  U2 = Transformer [package=transformer]
  D1 = P1000K [part_number=P1000K]
  LED1 = smd LED [color="Red (633nm)" package="0603 [SMD]"]

nets:
  N1: VCC4.-, U1.MAIN, Q2.1, Q4.1
  N2: VCC4.+, U1.COIL1, Q1.1, Q3.1, D1.cathode
  N3: U1.COIL2, D1.anode
  N4: U1.NC, Q1.0, Q2.0
  N5: U1.NO, Q3.0, Q4.0
  N6: Q1.2, Q4.2, U2.4
  N7: Q2.2, Q3.2, U2.3
  N8: U2.1, LED1.cathode
  N9: U2.2, LED1.anode
