# Fritzing sketch id4514_Scale_Sketch_0 (saved by Fritzing 0.9.3b)
breadboards: 1

parts:
  Part1 = Arduino Uno (Rev3)
  Part2 = SO-28W [chip_label=SO-28W package=SO(w)]
  U2 = OP37 - Low Noise, Precision, High Speed Op Amp [part_number=OP37]
  U3 = AD584 - Pin Programmable Precision Voltage Reference [part_number=AD584]
  R1 = Resistor [tolerance=±5% resistance=680 package=THT]

nets:
  N1: Part1.D10_PWM/SS, Part2.16
  N2: Part1.D11_PWM/MOSI, Part2.19
  N3: Part1.D12/MISO, Part2.17
  N4: Part1.D13/SCK, Part2.18
  N5: Part2.9, Part2.11, U2.NC, U2.V+, U3.VBG
  N6: Part2.10, Part2.12, Part2.15, U2.-V, U3.COMMON
  N7: Part2.20, U2.OUT
  N8: U2.TRIM#1, R1.Pin_1
  N9: U2.TRIM#8, R1.Pin_0
