# Fritzing sketch id4515_Steckplantinenansicht_0 (saved by Fritzing 0.9.3b)
breadboards: 1

parts:
  LCD1 = LCD screen
  Bauteil1 = Arduino Uno (Rev3)
  R1 = Trimmer Potentiometer [maximum_resistance=10kΩ package=THT]
  hc-sr1 = hc-sr04
  R2 = Resistor [tolerance=±5% resistance=220 package=THT]
  VCC1 = Battery  # not connected

nets:
  VSS: LCD1.VSS, LCD1.VDD, LCD1.LED+, Bauteil1.5V, R1.leg1, hc-sr1.VCC
  N1: LCD1.V0, R1.wiper
  N2: LCD1.RS, Bauteil1.D1/TX
  GND: LCD1.R/W, LCD1.LED-, Bauteil1.GND, R1.leg2, hc-sr1.GND, R2.Pin_0, R2.Pin_1
  N3: LCD1.E, Bauteil1.D2
  N4: LCD1.DB4, Bauteil1.D4
  N5: LCD1.DB5, Bauteil1.D5_PWM
  N6: LCD1.DB6, Bauteil1.D6_PWM
  N7: LCD1.DB7, Bauteil1.D7
  N8: Bauteil1.D9_PWM, hc-sr1.Trig
  N9: Bauteil1.D10_PWM/SS, hc-sr1.Echo

notes:
  W: 100 cm
  W: 40 inch
