# Fritzing sketch id4516_Wemos___gyroscope_0 (saved by Fritzing 0.9.3b)
circuit board: 2.57362cm x 2.53349cm

parts:
  J3 = male pin header, 8 pins [form="♂ (male)"]
  J2 = male pin header, 8 pins [form="♂ (male)"]
  MPU9250_MPU-1 = SparkFun IMU Breakout - MPU-9250 [part_number=" SEN-13762"]  # not connected
  5v/3v3 = Solder Jumper [package=sj_3]
  GY521 = male pin header, 8 pins [form="♂ (male)"]
  5v/ad0/Gnd = Solder Jumper [package=sj_3_paste1_2]
  Int/D6 = Solder Jumper [package=sj_2s]
  WeMos_D1_Mini1 = Wemos_vide
  6DOF_DIGITAL = IMU Digital Combo Board 6DOF

nets:
  N1: J3.pin1, 5v/3v3.3, 5v/ad0/Gnd.3, WeMos_D1_Mini1.3v3
  N2: J3.pin2, WeMos_D1_Mini1.d8
  N3: J3.pin3, WeMos_D1_Mini1.d7
  N4: J3.pin4, Int/D6.2, WeMos_D1_Mini1.d6
  N5: J3.pin5, WeMos_D1_Mini1.d5
  N6: J3.pin6, WeMos_D1_Mini1.d0
  N7: J3.pin7, WeMos_D1_Mini1.a0
  N8: J3.pin8, WeMos_D1_Mini1.rst
  N9: J2.pin1, 5v/3v3.1, WeMos_D1_Mini1.5v
  N10: J2.pin2, GY521.pin7, 5v/ad0/Gnd.1, WeMos_D1_Mini1.g, 6DOF_DIGITAL.GND
  N11: J2.pin3, GY521.pin5, WeMos_D1_Mini1.d4, 6DOF_DIGITAL.SDA
  N12: J2.pin4, GY521.pin6, WeMos_D1_Mini1.d3, 6DOF_DIGITAL.SCL
  N13: J2.pin5, WeMos_D1_Mini1.d2
  N14: J2.pin6, WeMos_D1_Mini1.d1
  N15: J2.pin7, WeMos_D1_Mini1.rx
  N16: J2.pin8, WeMos_D1_Mini1.tx
  N17: 5v/3v3.2, GY521.pin8, 6DOF_DIGITAL.3.3V
  N18: GY521.pin1, Int/D6.1
  N19: GY521.pin2, 5v/ad0/Gnd.2

notes:
  3V3 D8 D7 D6 D5 D0 A0 RST
  5V GND D4 D3 D2 D1 RX TX
  VCC GND SCL SDA XDA XCL AD0  INT
  VCC GND SDA SCL
  MPU5060
  MPU6050
  3v/5v
  gnd/ad0/3v
  Int/D6
  Gyroscope MPU6050
  pour Wemos D1 - v.1
  Julien Hogert - 2018
