# Fritzing sketch id4517_WS2350_0 (saved by Fritzing 0.7.11b)
breadboards: 1

parts:
  IC1 = IC, DIP package, 16 pins [chip_label=MAX232N]
  C1 = Electrolytic Capacitor [capacitance=10µF voltage=63V package="100 mil [THT, electrolytic]"]
  C2 = Ceramic Capacitor [capacitance=100nF voltage=63V package="100 mil [THT, multilayer]"]
  C3 = Electrolytic Capacitor [capacitance=10µF voltage=63V package="100 mil [THT, electrolytic]"]
  C4 = Electrolytic Capacitor [capacitance=10µF voltage=63V package="100 mil [THT, electrolytic]"]
  C5 = Electrolytic Capacitor [capacitance=10µF voltage=63V package="100 mil [THT, electrolytic]"]
  C6 = Electrolytic Capacitor [capacitance=10µF voltage=63V package="100 mil [THT, electrolytic]"]
  CN1 = DB9_rt_female
  CN2 = DB9_rt_female
  CN3 = DB9_rt_female
  Arduino_Ethernet_Shield1 = Arduino Ethernet Shield

nets:
  N1: IC1.pin1, C4.+
  N2: IC1.pin2, C3.-
  N3: IC1.pin3, C4.-
  N4: IC1.pin4, C5.+
  N5: IC1.pin5, C5.-
  N6: IC1.pin6, C6.+
  N7: IC1.pin7, CN1.connector7
  N8: IC1.pin8, CN1.connector6
  N9: IC1.pin9, CN1.connector3
  N10: IC1.pin10, Arduino_Ethernet_Shield1.D7
  N11: IC1.pin11, Arduino_Ethernet_Shield1.D2
  N12: IC1.pin12, Arduino_Ethernet_Shield1.D3
  N13: IC1.pin13, CN1.connector2
  N14: IC1.pin14, CN1.connector1
  N15: IC1.pin15, C1.+, C2.1, C6.-, CN1.connector4, Arduino_Ethernet_Shield1.GND
  N16: IC1.pin16, C1.-, C2.0, C3.+, Arduino_Ethernet_Shield1.+5V
  N17: CN2.connector1, CN3.connector2
  N18: CN2.connector2, CN3.connector1
  N19: CN2.connector3, CN3.connector3
  N20: CN2.connector4, CN3.connector4
  N21: CN2.connector6, Arduino_Ethernet_Shield1.D5
  N22: CN2.connector7, CN3.connector6

notes:
  Anschluss Wetterstation
