# Fritzing sketch id4518_SWv1_0 (saved by Fritzing 0.9.3b)
circuit board: 8.46667cm x 5.64444cm

parts:
  U1 = ESP8266 WiFi Module [part_number=ESP8266]
  Grove1 = Grove OLED 128x96
  JP1 = Header 6 [package=1x06-smd]
  U2 = LIPO-2000mAh [package=lipo-2000]
  S1 = SWITCH-MOMENTARY-2 [package=tactile-pth-12mm]
  S2 = SWITCH-MOMENTARY-2 [package=tactile-pth-12mm]

nets:
  N1: U1.RXD, JP1.3
  VCC: U1.VCC, Grove1.VCC, JP1.1
  GND: U1.GND, Grove1.GND, JP1.2, S1.2, S2.2
  N2: U1.GPIO_4, Grove1.SCL
  N3: U1.GPIO_5, Grove1.SDA
  N4: U1.GPIO_12, S2.1
  N5: U1.GPIO_13, S1.1
  N6: JP1.5, U2.-
  N7: JP1.6, U2.+
