# Fritzing sketch id451_Untitled_Sketch_3_0 (saved by Fritzing 0.9.3b)
breadboards: 1

parts:
  Part1 = Arduino Uno (Rev3)
  U1 = LCD-16X2 [package=lcd-16x2]
  hc-sr1 = hc-sr04

nets:
  N1: Part1.A0, hc-sr1.Trig
  N2: Part1.A1, hc-sr1.Echo
  N3: Part1.D11_PWM/MOSI, U1.E
  N4: Part1.D12/MISO, U1.RS
  N5: Part1.D2, U1.DB7
  N6: Part1.D3_PWM, U1.DB6
  N7: Part1.D4, U1.DB5
  N8: Part1.D5_PWM, U1.DB4
  5V: Part1.5V, U1.VDD, U1.A, hc-sr1.VCC
  GND: Part1.GND, U1.VSS, U1.R_W, U1.K, hc-sr1.GND
