# Fritzing sketch id4520_Whack_a_Mole_0 (saved by Fritzing 0.9.3b)
breadboards: 2

parts:
  Part1 = Arduino Mega 2560 (Rev3)
  LED1 = LED - 5mm [color="Blue (430nm)" package="5 mm [THT]"]
  S1 = Pushbutton [package="[THT]"]
  S2 = Pushbutton [package="[THT]"]
  S3 = Pushbutton [package="[THT]"]
  S4 = Pushbutton [package="[THT]"]
  S5 = Pushbutton [package="[THT]"]
  LED2 = LED - 5mm [color="Blue (430nm)" package="5 mm [THT]"]
  LED3 = LED - 5mm [color="Blue (430nm)" package="5 mm [THT]"]
  LED4 = LED - 5mm [color="Blue (430nm)" package="5 mm [THT]"]
  LED5 = LED - 5mm [color="Blue (430nm)" package="5 mm [THT]"]
  R1 = Resistor [tolerance=±5% resistance=220 package=THT]
  R2 = Resistor [tolerance=±5% resistance=220 package=THT]
  R3 = Resistor [tolerance=±5% resistance=220 package=THT]
  R4 = Resistor [tolerance=±5% resistance=220 package=THT]
  R5 = Resistor [tolerance=±5% resistance=220 package=THT]
  R6 = Resistor [tolerance=±5% resistance=330 package=THT]
  R7 = Resistor [tolerance=±5% resistance=330 package=THT]
  R8 = Resistor [tolerance=±5% resistance=330 package=THT]
  R9 = Resistor [tolerance=±5% resistance=330 package=THT]
  R10 = Resistor [tolerance=±5% resistance=330 package=THT]
  LED6 = LED - 5mm [color="Green (555nm)" package="5 mm [THT]"]
  LED7 = LED - 5mm [color="Red (633nm)" package="5 mm [THT]"]
  LED8 = LED - 5mm [color="Yellow (585nm)" package="5 mm [THT]"]
  R11 = Resistor [tolerance=±5% resistance=220 package=THT]
  R12 = Resistor [tolerance=±5% resistance=220 package=THT]
  R13 = Resistor [tolerance=±5% resistance=220 package=THT]
  J1 = Piezo Speaker
  7_Segment1 = 7 Segment Display
  R14 = Resistor [tolerance=±5% resistance=220 package=THT]
  R15 = Resistor [tolerance=±5% resistance=220 package=THT]
  R16 = Resistor [tolerance=±5% resistance=220 package=THT]
  R17 = Resistor [tolerance=±5% resistance=220 package=THT]
  R18 = Resistor [tolerance=±5% resistance=220 package=THT]
  R19 = Resistor [tolerance=±5% resistance=220 package=THT]
  R20 = Resistor [tolerance=±5% resistance=220 package=THT]
  7_Segment2 = 7 Segment Display
  7_Segment3 = 7 Segment Display
  R21 = Resistor [tolerance=±5% resistance=220 package=THT]
  R22 = Resistor [tolerance=±5% resistance=220 package=THT]
  R23 = Resistor [tolerance=±5% resistance=220 package=THT]
  R24 = Resistor [tolerance=±5% resistance=220 package=THT]
  R25 = Resistor [tolerance=±5% resistance=220 package=THT]
  R26 = Resistor [tolerance=±5% resistance=220 package=THT]
  R27 = Resistor [tolerance=±5% resistance=220 package=THT]
  R28 = Resistor [tolerance=±5% resistance=220 package=THT]
  R29 = Resistor [tolerance=±5% resistance=220 package=THT]
  R30 = Resistor [tolerance=±5% resistance=220 package=THT]
  R31 = Resistor [tolerance=±5% resistance=220 package=THT]
  R32 = Resistor [tolerance=±5% resistance=220 package=THT]
  R33 = Resistor [tolerance=±5% resistance=220 package=THT]
  R34 = Resistor [tolerance=±5% resistance=220 package=THT]
  R35 = Resistor [tolerance=±5% resistance=220 package=THT]
  R36 = Resistor [tolerance=±5% resistance=220 package=THT]

nets:
  N1: Part1.D13_PWM, LED1.anode
  N2: Part1.D12_PWM, LED2.anode
  N3: Part1.D11_PWM, LED3.anode
  N4: Part1.D10_PWM, LED4.anode
  N5: Part1.D9_PWM, LED5.anode
  N6: Part1.D8_PWM, J1.pin2
  N7: Part1.5V, S1.Pin_1, S1.Pin_2, S2.Pin_1, S2.Pin_2, S3.Pin_1, S3.Pin_2, S4.Pin_1, S4.Pin_2, S5.Pin_1, S5.Pin_2
  N8: Part1.GND, R1.Pin_0, R2.Pin_0, R3.Pin_0, R4.Pin_0, R5.Pin_0, R6.Pin_0, R7.Pin_0, R8.Pin_0, R9.Pin_0, R10.Pin_0, R11.Pin_0, R12.Pin_0, R13.Pin_0, J1.pin1, R24.Pin_1, R36.Pin_0
  N9: Part1.D3_PWM, S1.Pin_3, S1.Pin_4, R10.Pin_1
  N10: Part1.D4_PWM, S2.Pin_3, S2.Pin_4, R9.Pin_1
  N11: Part1.D5_PWM, S3.Pin_3, S3.Pin_4, R8.Pin_1
  N12: Part1.D6_PWM, S4.Pin_3, S4.Pin_4, R7.Pin_1
  N13: Part1.D7_PWM, S5.Pin_3, S5.Pin_4, R6.Pin_1
  N14: Part1.D22, Part1.D23, Part1.D24, R18.Pin_1, R19.Pin_1, R20.Pin_1
  N15: Part1.D25, Part1.D26, Part1.D27, Part1.D28, R14.Pin_0, R15.Pin_0, R16.Pin_0, R17.Pin_0
  N16: Part1.D29, Part1.D30, Part1.D31, R25.Pin_1, R26.Pin_1, R27.Pin_1
  N17: Part1.D32, Part1.D33, Part1.D34, Part1.D35, R21.Pin_0, R22.Pin_0, R23.Pin_0, R28.Pin_0
  N18: Part1.D36, Part1.D37, Part1.D38, R31.Pin_1, R32.Pin_1, R33.Pin_1
  N19: Part1.D39, Part1.D40, Part1.D41, Part1.D42, R29.Pin_0, R30.Pin_0, R34.Pin_0, R35.Pin_0
  N20: Part1.D50, LED6.anode
  N21: Part1.D52, LED8.anode
  N22: Part1.D53, LED7.anode
  N23: LED1.cathode, R1.Pin_1
  N24: LED2.cathode, R2.Pin_1
  N25: LED3.cathode, R3.Pin_1
  N26: LED4.cathode, R4.Pin_1
  N27: LED5.cathode, R5.Pin_1
  N28: LED6.cathode, R11.Pin_1
  N29: LED7.cathode, R12.Pin_1
  N30: LED8.cathode, R13.Pin_1
  N31: 7_Segment1.Segment_G, 7_Segment1.Segment_F, 7_Segment1.common_anode, 7_Segment1.Segment_E, 7_Segment1.Segment_D, 7_Segment1.Segment_DP, 7_Segment1.Segment_C, 7_Segment1.Segment_B, 7_Segment1.Segment_A, R14.Pin_1, R15.Pin_1, R16.Pin_1, R17.Pin_1, R18.Pin_0, R19.Pin_0, R20.Pin_0, 7_Segment2.Segment_G, 7_Segment2.Segment_F, 7_Segment2.common_anode, 7_Segment2.Segment_E, 7_Segment2.Segment_D, 7_Segment2.Segment_DP, 7_Segment2.Segment_C, 7_Segment2.Segment_B, 7_Segment2.Segment_A, 7_Segment3.Segment_G, 7_Segment3.Segment_F, 7_Segment3.common_anode, 7_Segment3.Segment_E, 7_Segment3.Segment_D, 7_Segment3.Segment_DP, 7_Segment3.Segment_C, 7_Segment3.Segment_B, 7_Segment3.Segment_A, R21.Pin_1, R22.Pin_1, R23.Pin_1, R24.Pin_0, R25.Pin_0, R26.Pin_0, R27.Pin_0, R28.Pin_1, R29.Pin_1, R30.Pin_1, R31.Pin_0, R32.Pin_0, R33.Pin_0, R34.Pin_1, R35.Pin_1, R36.Pin_1
