# Fritzing sketch id4525_WhiteboardCircuit_0 (saved by Fritzing 0.8.5b)
breadboards: 1

parts:
  Part2 = EasyDriver_v44
  Part3 = EasyDriver_v44
  J1 = single row smd female pin header, 2 pins [form="♀ (female)"]
  M1 = Stepper Motor - Bipolar
  M2 = Stepper Motor - Bipolar
  Part1 = Arduino Uno (Rev3)

nets:
  GND: Part2.GND, Part3.GND, J1.pin2, Part1.GND
  N1: Part2.V+, Part3.V+, J1.pin1
  N2: Part2.STEP, Part1.D13/SCK
  N3: Part2.DIR, Part1.D12/MISO
  N4: Part2.OUT2A, M1.D
  N5: Part2.OUT2B, M1.C
  N6: Part2.OUT1A, M1.A
  N7: Part2.OUT1B, M1.B
  N8: Part3.STEP, Part1.D10_PWM/SS
  N9: Part3.DIR, Part1.D9_PWM
  N10: Part3.OUT2A, M2.D
  N11: Part3.OUT2B, M2.C
  N12: Part3.OUT1A, M2.A
  N13: Part3.OUT1B, M2.B
