# Fritzing sketch id4526_Quizzettone_a_4_0 (saved by Fritzing 0.7.12b)
breadboards: 1

parts:
  LED2 = LED - 5mm [color="Red (633nm)" package="5 mm [THT]"]
  LED4 = LED - 5mm [color="Yellow (595nm)" package="5 mm [THT]"]
  LED1 = LED - 5mm [color="Blue (430nm)" package="5 mm [THT]"]
  LED3 = LED - 5mm [color="Green (555nm)" package="5 mm [THT]"]
  Porte_NOR = PICAXE-14M [package=THT]
  Porte_OR = PICAXE-14M [package=THT]
  Power_plug = Power plug
  part = female pin header, 1 pin [form="♀ (female)"]
  part_2 = female pin header, 1 pin [form="♀ (female)"]
  P1 = female pin header, 1 pin [form="♀ (female)"]  # not connected
  part_3 = female pin header, 1 pin [form="♀ (female)"]  # not connected
  P4 = female pin header, 1 pin [form="♀ (female)"]
  part_4 = female pin header, 1 pin [form="♀ (female)"]
  part_5 = female pin header, 1 pin [form="♀ (female)"]  # not connected
  part_6 = female pin header, 1 pin [form="♀ (female)"]  # not connected
  P2 = female pin header, 1 pin [form="♀ (female)"]
  part_7 = female pin header, 1 pin [form="♀ (female)"]
  part_8 = female pin header, 1 pin [form="♀ (female)"]  # not connected
  part_9 = female pin header, 1 pin [form="♀ (female)"]  # not connected
  P3 = female pin header, 1 pin [form="♀ (female)"]
  part_10 = female pin header, 1 pin [form="♀ (female)"]
  part_11 = female pin header, 1 pin [form="♀ (female)"]  # not connected
  part_12 = female pin header, 1 pin [form="♀ (female)"]  # not connected
  330 = Resistor [tolerance=±5% resistance=220 package=THT]
  330_2 = Resistor [tolerance=±5% resistance=220 package=THT]
  330_3 = Resistor [tolerance=±5% resistance=220 package=THT]
  330_4 = Resistor [tolerance=±5% resistance=220 package=THT]

nets:
  GND: LED2.cathode, LED4.cathode, LED1.cathode, LED3.cathode, Porte_NOR.In_0_/_ADC_0, Porte_OR.In_0_/_ADC_0, Power_plug.GND
  N1: LED2.anode, 330_4.Pin_1
  N2: LED4.anode, 330_3.Pin_1
  N3: LED1.anode, 330_2.Pin_1
  N4: LED3.anode, 330.Pin_1
  N5: Porte_NOR.+V, Porte_OR.In_4_/_ADC_4
  N6: Porte_NOR.Serial_In, Porte_OR.Out_5, Porte_OR.Out_1, part_4.pin1, 330_3.Pin_0
  N7: Porte_NOR.In_4_/_ADC_4, P3.pin1
  N8: Porte_NOR.In_3_/_Infrain, P4.pin1
  N9: Porte_NOR.In_2, Porte_OR.Out_4, Porte_OR.Serial_Out_/_Out_0_/_Infraout, part_10.pin1, 330.Pin_0
  N10: Porte_NOR.In_1, Porte_OR.In_3_/_Infrain
  N11: Porte_NOR.Out_5, Porte_OR.Out_3
  N12: Porte_NOR.Out_4, Porte_OR.+V, Porte_OR.In_2, part.pin1, 330_2.Pin_0
  N13: Porte_NOR.Out_3, P2.pin1
  N14: Porte_NOR.Out_2, part_2.pin1
  N15: Porte_NOR.Out_1, Porte_OR.Out_2
  N16: Porte_NOR.Serial_Out_/_Out_0_/_Infraout, Porte_OR.Serial_In, Porte_OR.In_1, part_7.pin1, 330_4.Pin_0
  5V: Porte_NOR.0V, Porte_OR.0V, Power_plug.VCC
