# Fritzing sketch id4527_WiCuBoBS_0 (saved by Fritzing 0.7.4b)
breadboards: 2

parts:
  Arduino1 = Arduino
  LCD1 = LCD screen
  U1 = XBee
  S1 = Pushbutton [package="[THT]"]
  R1 = Rotary Potentiometer (Small) [maximum_resistance=100kΩ]
  R2 = Resistor [tolerance=±5% resistance=220 package=THT]
  Arduino2 = Arduino
  LED1 = LED - 5mm [color="Red (633nm)" package="5 mm [THT]"]
  LED2 = LED - 5mm [color="Red (633nm)" package="5 mm [THT]"]
  LED3 = LED - 5mm [color="Red (633nm)" package="5 mm [THT]"]
  LED4 = LED - 5mm [color="Red (633nm)" package="5 mm [THT]"]
  LED5 = LED - 5mm [color="Red (633nm)" package="5 mm [THT]"]
  LED6 = LED - 5mm [color="Red (633nm)" package="5 mm [THT]"]
  LED7 = LED - 5mm [color="Red (633nm)" package="5 mm [THT]"]
  LED8 = LED - 5mm [color="Red (633nm)" package="5 mm [THT]"]
  LED9 = LED - 5mm [color="Red (633nm)" package="5 mm [THT]"]
  LED10 = LED - 5mm [color="Red (633nm)" package="5 mm [THT]"]
  U2 = XBee

nets:
  GND: Arduino1.GND, LCD1.DB1, U1.GND, R1.leg2, R2.Pin_1
  +5V: Arduino1.D2, Arduino1.+5V, LCD1.DB0, U1.VCC, S1.Pin_3, S1.Pin_4, R1.leg1, R2.Pin_0
  N1: Arduino1.D1TX, U1.pin3
  N2: Arduino1.D0RX, U1.pin4
  N3: Arduino1.A3, R1.wiper
  N4: Arduino1.A4, LCD1.VSS
  N5: Arduino1.A5, LCD1.VDD
  N6: Arduino2.GND, LED1.anode, LED2.anode, LED3.anode, LED4.anode, LED5.anode, LED6.anode, LED7.anode, LED8.anode, LED9.anode, LED10.anode, U2.pin12
  N7: Arduino2.D11, LED2.cathode
  N8: Arduino2.D10, LED3.cathode
  N9: Arduino2.D9, LED4.cathode
  N10: Arduino2.D8, LED5.cathode
  N11: Arduino2.D7, LED6.cathode
  N12: Arduino2.D6, LED7.cathode
  N13: Arduino2.D5, LED8.cathode
  N14: Arduino2.D4, LED9.cathode
  N15: Arduino2.D3, LED10.cathode
  N16: Arduino2.D2, LED1.cathode
  N17: Arduino2.D1TX, U2.pin19
  N18: Arduino2.D0RX, U2.pin20
  N19: Arduino2.+5V, U2.pin11
