# Fritzing sketch id4528_WifiCanonBulb_ALIM_0 (saved by Fritzing 0.9.3b)

parts:
  R1 = Resistor [tolerance=±5% resistance=1k package=THT]
  R3 = Trimmer Potentiometer [maximum_resistance=2kΩ package=THT]
  OUTPUT = male pin header, 3 pins [form="♂ (male)"]
  C1 = Electrolytic Capacitor [capacitance=100µF package="100 mil [THT, electrolytic]"]
  78ADJ_3_3V = Voltage Regulator [package=to220-adj]
  INPUT = female pin header, 2 pins [form="♀ (female)"]

nets:
  N1: R1.Pin_0, OUTPUT.pin2, C1.+, 78ADJ_3_3V.OUT
  N2: R1.Pin_1, R3.leg2, 78ADJ_3_3V.ADJ
  GND: R3.wiper, OUTPUT.pin1, C1.-, INPUT.pin2
  N3: OUTPUT.pin3, 78ADJ_3_3V.IN, INPUT.pin1

notes:
  < +5V
  > GND
  ALIMENTAZIONE
  +5V <
  GND >
  +3.3V <
