# Fritzing sketch id4529_WifiCanonBulb_ESP01_0 (saved by Fritzing 0.9.3b)
circuit board: 8.46667cm x 5.64444cm

parts:
  ESP-01_INTERFACCIA_B = female pin header, 4 pins [form="♀ (female)"]
  CANON = female pin header, 3 pins [form="♀ (female)"]
  LED_WS2812 = female pin header, 3 pins [form="♀ (female)"]
  RESET = Pushbutton [package="[THT]"]
  OPT_SCATTO = Sharp PC817 [package=THT]
  OPT_FUOCO = Sharp PC817 [package=THT]
  R_FUOCO = Resistor [tolerance=±5% resistance=100 package=THT]
  R_SCATTO = Resistor [tolerance=±5% resistance=100 package=THT]
  ESP-01_ALIMENTAZIONE = female pin header, 3 pins [form="♀ (female)"]
  PIN_0 = male pin header, 3 pins [form="♂ (male)"]
  R_ESP-01_CHP = Resistor [tolerance=±5% resistance=1k package=THT]
  ESP-01_INTERFACCIA_A = female pin header, 4 pins [form="♀ (female)"]

nets:
  3.3V: ESP-01_INTERFACCIA_B.pin1, OPT_SCATTO.Pin_1, OPT_FUOCO.Pin_1, ESP-01_ALIMENTAZIONE.pin2, PIN_0.pin2, R_ESP-01_CHP.Pin_1
  N1: ESP-01_INTERFACCIA_B.pin2, RESET.Pin_1, RESET.Pin_2
  N2: ESP-01_INTERFACCIA_B.pin3, R_ESP-01_CHP.Pin_0
  N3: ESP-01_INTERFACCIA_B.pin4, R_SCATTO.Pin_1
  N4: CANON.pin1, OPT_SCATTO.Pin_4
  N5: CANON.pin2, OPT_FUOCO.Pin_4
  N6: CANON.pin3, OPT_SCATTO.Pin_3, OPT_FUOCO.Pin_3
  GND: LED_WS2812.pin1, RESET.Pin_3, RESET.Pin_4, ESP-01_ALIMENTAZIONE.pin3, PIN_0.pin3, ESP-01_INTERFACCIA_A.pin4
  N7: LED_WS2812.pin2, ESP-01_INTERFACCIA_A.pin3
  5V: LED_WS2812.pin3, ESP-01_ALIMENTAZIONE.pin1
  N8: OPT_SCATTO.Pin_2, R_SCATTO.Pin_0
  N9: OPT_FUOCO.Pin_2, R_FUOCO.Pin_1
  N10: R_FUOCO.Pin_0, ESP-01_INTERFACCIA_A.pin1
  N11: PIN_0.pin1, ESP-01_INTERFACCIA_A.pin2

notes:
  > LED WS2812
  < RESET
  ALIMENTAZIONE
  < +5V
  ESP-01 >
  < +3.3V
  > GND
  < GND
  > +5V
  < SCATTO
  < FUOCO
