# Fritzing sketch id452_CNC_fritz_0 (saved by Fritzing 0.9.3b)
breadboards: 1

parts:
  Composant1 = Arduino Uno (Rev3)
  Pololu_A1 = Pololu A4988 [package=SO16]
  Pololu_A2 = Pololu A4988 [package=SO16]
  Pololu_A3 = Pololu A4988 [package=SO16]
  C2 = Electrolytic Capacitor [capacitance=47µF package="0807 [SMD, electrolytic]"]
  S1 = Pushbutton [package="[THT]"]  # not connected
  S2 = Pushbutton [package="[THT]"]  # not connected
  S3 = Pushbutton [package="[THT]"]  # not connected
  S4 = Pushbutton [package="[THT]"]  # not connected
  Power_plug1 = Power plug
  M1 = Stepper Motor - Bipolar
  M2 = Stepper Motor - Bipolar
  M3 = Stepper Motor - Bipolar
  C3 = Electrolytic Capacitor [capacitance=47µF package="0807 [SMD, electrolytic]"]
  C4 = Electrolytic Capacitor [capacitance=47µF package="0807 [SMD, electrolytic]"]
  S5 = Pushbutton [package="[THT]"]  # not connected
  S6 = Pushbutton [package="[THT]"]  # not connected
  R2 = Rotary Potentiometer (Large) [maximum_resistance=10kΩ package=THT]
  U4 = JOYSTICK-PSP1000 [package=joystick-psp1000]  # not connected
  R3 = Resistor [tolerance=±5% resistance=220 package=THT]

nets:
  N1: Composant1.A1, R2.wiper, R2.leg2, R3.Pin_1
  N2: Composant1.D9_PWM, Pololu_A2.STEP
  N3: Composant1.D10_PWM/SS, Pololu_A2.DIR
  N4: Composant1.D11_PWM/MOSI, Pololu_A3.STEP
  N5: Composant1.D12/MISO, Pololu_A3.DIR
  N6: Composant1.D6_PWM, Pololu_A1.STEP
  N7: Composant1.D7, Pololu_A1.DIR
  VDD: Composant1.5V, Pololu_A1.VDD, Pololu_A2.VDD, Pololu_A3.VDD, R2.leg1
  GND: Composant1.GND, Pololu_A1.GND, Pololu_A2.GND, Pololu_A3.GND, C2.+, Power_plug1.GND, C3.+, C4.+, R3.Pin_0
  N8: Pololu_A1.RESET, Pololu_A1.SLEEP
  N9: Pololu_A1.1B, M1.D
  N10: Pololu_A1.1A, M1.B
  N11: Pololu_A1.2A, M1.C
  N12: Pololu_A1.2B, M1.A
  N13: Pololu_A1.VMOT, Pololu_A2.VMOT, Pololu_A3.VMOT, C2.-, Power_plug1.VCC, C3.-, C4.-
  N14: Pololu_A2.RESET, Pololu_A2.SLEEP
  N15: Pololu_A2.1B, M3.D
  N16: Pololu_A2.1A, M3.B
  N17: Pololu_A2.2A, M3.C
  N18: Pololu_A2.2B, M3.A
  N19: Pololu_A3.RESET, Pololu_A3.SLEEP
  N20: Pololu_A3.1B, M2.D
  N21: Pololu_A3.1A, M2.B
  N22: Pololu_A3.2A, M2.C
  N23: Pololu_A3.2B, M2.A
