# Fritzing sketch id4531_OAP_sense_2d_wifly_uno_0 (saved by Fritzing 0.7.11b)
breadboards: 1

parts:
  Arduino1 = Arduino
  Part1 = Arduino WiFly Shield
  R1 = Resistor [tolerance=±5% resistance=220 package=THT]
  LED_Left = LED - 5mm [color="Orange (620nm)" package="5 mm [THT]"]
  LED_Right = LED - 5mm [color="Red (633nm)" package="5 mm [THT]"]
  R2 = Resistor [tolerance=±5% resistance=220 package=THT]
  S1_Left = Reed switch [package=THT]
  S2_Right = Reed switch [package=THT]
  U1 = mystery part, 5 pins [chip_label=KIT-10733]

nets:
  N1: Arduino1.VIN, U1.pin5
  N2: Part1.5V, U1.pin3
  N3: Part1.D3, S1_Left.pin_2
  N4: Part1.D5, S2_Right.pin_2
  N5: Part1.D6, R1.Pin_0
  N6: Part1.D7, U1.pin2
  N7: Part1.D9, R2.Pin_1
  N8: Part1.GND, LED_Left.cathode, LED_Right.cathode, S1_Left.pin_1, S2_Right.pin_1, U1.pin1
  N9: Part1.VIN, U1.pin4
  N10: R1.Pin_1, LED_Left.anode
  N11: LED_Right.anode, R2.Pin_0

notes:
  Cut the header pin VIN so that power routes through the grey wire in this circuit
