# Fritzing sketch id4532_ESP8226AsSerialMonitor_0 (saved by Fritzing 0.9.3b)
breadboards: 2

parts:
  Bauteil1 = Arduino Nano (Rev3.0)
  WeMos_D1_Mini1 = WeMos D1 Mini
  R1 = Resistor [tolerance=±5% resistance=1 package=THT]
  R2 = Resistor [tolerance=±5% resistance=2.0k package=THT]

nets:
  N1: Bauteil1.D1/TX, R1.Pin_0
  N2: Bauteil1.GND, WeMos_D1_Mini1.G, R2.Pin_1
  5V: Bauteil1.5V, WeMos_D1_Mini1.5V
  N3: WeMos_D1_Mini1.D7, R1.Pin_1, R2.Pin_0
