# Fritzing sketch id4534_LH02Fritzing_eskema_0 (saved by Fritzing 0.9.3b)

parts:
  Part1 = Arduino Uno (Rev3)
  J1 = Basic Servo
  U1 = Barometric Pressure Sensor

nets:
  N1: Part1.A4/SDA, U1.connector6
  N2: Part1.A5/SCL, U1.connector7
  N3: Part1.D9_PWM, J1.pulse
  N4: Part1.3V3, U1.connector5
  5V: Part1.5V, J1.vcc
  GND: Part1.GND, J1.gnd, U1.connector4
