# Fritzing sketch id4535_Wilbert_Salta_Obstaculos_0 (saved by Fritzing 0.9.2b)
breadboards: 1

parts:
  LCD1 = LCD screen
  S1 = Pushbutton [package="[THT]"]
  Parte1 = Arduino Uno (Rev3)

nets:
  VSS: LCD1.VSS, LCD1.V0, LCD1.R/W, LCD1.LED-, S1.Pin_3, Parte1.GND
  VDD: LCD1.VDD, Parte1.5V
  N1: LCD1.RS, Parte1.D11_PWM/MOSI
  N2: LCD1.E, Parte1.D9_PWM
  N3: LCD1.DB4, Parte1.D6_PWM
  N4: LCD1.DB5, Parte1.D5_PWM
  N5: LCD1.DB6, Parte1.D4
  N6: LCD1.DB7, Parte1.D3_PWM
  N7: S1.Pin_1, Parte1.D2
