# Fritzing sketch id4536_wildcat_0 (saved by Fritzing 0.9.3b)
circuit board: 8.46667cm x 5.64444cm
breadboards: 1

parts:
  Part1 = adafruit [part_number="Adafruit #2821"]
  S3 = Momentary Switch [package=ksa_sealed_tac_switch]

nets:
  N1: Part1.connector53, S3.1
  N2: Part1.connector66, S3.3

notes:
  The 16x8 LED featherwing fits on top of the feather huzzah when in use.
  I've only placed it to one side here to show the huzzah on the diagram.
