# Fritzing sketch id4538_senior_project_0 (saved by Fritzing 0.9.3b)
breadboards: 1

parts:
  Part1 = Arduino Uno (Rev3)
  R1 = Resistor [tolerance=±5% resistance=220 package=THT]
  R2 = Resistor [tolerance=±5% resistance=220 package=THT]
  U1 = SHT1x Humdity Sensor [package=sht1x]
  Part3 = adafruit [part_number="Adafruit #2019"]
  Part4 = adafruit [part_number="Adafruit #254"]
  VCC1 = Battery block 9V  # not connected

nets:
  N1: Part1.A4/SDA, Part3.connector11
  N2: Part1.A5/SCL, Part3.connector12
  N3: Part1.D10_PWM/SS, Part4.connector38
  N4: Part1.D11_PWM/MOSI, Part4.connector37
  N5: Part1.D12/MISO, Part4.connector36
  N6: Part1.D13/SCK, Part4.connector35
  N7: Part1.D2, R1.Pin_0
  N8: Part1.D6_PWM, U1.DATA
  N9: Part1.D7, U1.GND
  5V: Part1.5V, R1.Pin_1, R2.Pin_0, U1.VDD, Part3.connector17, Part4.connector32
  N10: Part1.GND, U1.SCK, Part3.connector16, Part4.connector34

notes:
  Adafruit MMA8451
  Adafruit MicroSD
  Breakout Card
  SHT10 Temp/Humid
  Sensor
  A nemometer Wires
  Red=Ground Yellow=Power
  Black=Wind Speed
  Green=Direction
