# Fritzing sketch id4539_runner_driver_0 (saved by Fritzing 0.8.7b)
breadboards: 1

parts:
  LED2 = LED - 5mm [color="Red (633nm)" package="5 mm [THT]"]
  LED3 = LED - 5mm [color="Red (633nm)" package="5 mm [THT]"]
  LED4 = LED - 5mm [color="Red (633nm)" package="5 mm [THT]"]
  LED5 = LED - 5mm [color="Red (633nm)" package="5 mm [THT]"]
  Q1 = TIP120_Hi_Current_Darlington_Transistor [part_number=TIP120]
  FLORA1 = Adafruit_Flora
  R1 = Resistor [tolerance=±5% resistance=1k package=THT]
  U1 = TRANSISTOR_NPN_2 [part_number=2N2222 package=to-92]
  R2 = Resistor [tolerance=±5% resistance=220 package=THT]
  R3 = Resistor [tolerance=±5% resistance=1.5k package=THT]
  S2 = Round Pushbutton
  V1 = DC Power [voltage=5V part_number="5V 2A Supply"]

nets:
  N1: LED2.cathode, LED3.cathode, LED4.cathode, LED5.cathode, Q1.connector2
  N2: LED2.anode, LED3.anode, LED4.anode, LED5.anode, FLORA1.connector8, R2.Pin_0, S2.leg0, V1.V+
  N3: Q1.connector1, R1.Pin_1
  N4: Q1.connector3, FLORA1.connector1
  N5: FLORA1.connector2, R3.Pin_1
  N6: FLORA1.connector7, V1.V-
  N7: FLORA1.connector10, R1.Pin_0
  N8: U1.C, R2.Pin_1
  N9: U1.B, S2.leg1
  N10: U1.E, R3.Pin_0

notes:
  1 "channel"
  on pin d6
  per channel
  mA = led * 20
  (~20 leds/channel)
  total
  mA = add per channel
  (4 channels)
  Repeat for each channel (x4)
  R1 1kΩ - 10kΩ
  SCL is digital D3
  The switch is
  your finger
  Digital pin D3
  no switch,
  just bare wires (thread)
  for you fingers
  ~5ma @ 3V
  5V 2A
  Power Supply
  to "rails"
