# Fritzing sketch id453_tracker_solaire_0 (saved by Fritzing 0.9.3b)

parts:
  Composant1 = Arduino Uno (Rev3)
  J1 = Basic Servo
  J2 = Basic Servo
  R1 = Resistor [tolerance=±5% resistance=220 package="2512 [SMD]"]
  R2 = Resistor [tolerance=±5% resistance=220 package="2512 [SMD]"]
  R3 = Resistor [tolerance=±5% resistance=220 package="2512 [SMD]"]
  R4 = PHOTOCELL [package=photocell-kit]
  R5 = PHOTOCELL [package=photocell-kit]
  R6 = PHOTOCELL [package=photocell-kit]

nets:
  GND: Composant1.GND, J1.gnd, J2.gnd, R4.P$1, R5.P$1, R6.P$1
  N1: Composant1.D6_PWM, J1.pulse
  N2: Composant1.D7, J2.pulse
  VCC: Composant1.5V, J1.vcc, J2.vcc, R1.Pin_1, R2.Pin_1, R3.Pin_1
  N3: R1.Pin_0, R5.P$2
  N4: R2.Pin_0, R6.P$2
  N5: R3.Pin_0, R4.P$2
