# Fritzing sketch id4540_MPB_with_gnd_plane__FINAL_rev_5_0 (saved by Fritzing 0.9.2b)
circuit board: 15.24cm x 10.16cm
breadboards: 1

parts:
  U2 = IC, DIP package, 8 pins [chip_label=IC]
  U3 = IC, DIP package, 8 pins [chip_label=IC]  # not connected
  U1 = IC, DIP package, 20 pins [chip_label=IC]  # not connected
  U4 = IC, DIP package, 8 pins [chip_label=IC]  # not connected
  Pad1 = Pad [width=19.4863271793117 height=5.09579980343079 connect=center]
  U4_2 = IC, DIP package, 8 pins [chip_label=IC]  # not connected
  Pad3 = Pad [width=19.4863271793117 height=5.09579980343079 connect=center]
  U1_2 = IC, DIP package, 20 pins [chip_label=IC]  # not connected
  U3_2 = IC, DIP package, 8 pins [chip_label=IC]  # not connected
  U2_2 = IC, DIP package, 8 pins [chip_label=IC]

nets:
  N1: U2.pin2, U2.pin3, Pad1.pad
  N2: Pad3.pad, U2_2.pin2, U2_2.pin3

notes:
  1
  +
  X4
  CERN OHL v1.2
  7/18/15
  X7
  X8
  X9
  LED
