# Fritzing sketch id4541_Micke5_0 (saved by Fritzing 0.9.2b)
circuit board: 5.3435cm x 3.44947cm

parts:
  NANO = Arduino Nano (Rev3.0)
  J4 = female pin header, 4 pins [form="♀ (female)"]
  J2 = female pin header, 4 pins [form="♀ (female)"]
  4_7K = Resistor [tolerance=±5% resistance=220 package=THT]
  RJ12_1WIRE = RJ11 Jack [package=rj11-6]
  DS1820 = screw terminal, 3 pins
  J5 = female pin header, 4 pins [form="♀ (female)"]

nets:
  N1: NANO.GND, J2.pin1, RJ12_1WIRE.2, DS1820.pin3, J5.pin2
  N2: NANO.D2, 4_7K.Pin_1, RJ12_1WIRE.3, DS1820.pin2
  N3: NANO.D7, J2.pin2
  N4: NANO.D8, J4.pin2
  N5: NANO.D11/MOSI, J4.pin3
  N6: NANO.D12/MISO, J2.pin4
  N7: NANO.5V, 4_7K.Pin_0, RJ12_1WIRE.1, DS1820.pin1, J5.pin1
  N8: NANO.A5, J5.pin3
  N9: NANO.A4, J5.pin4
  N10: NANO.3V3, J4.pin1
  N11: NANO.D13/SCK, J2.pin3

notes:
  NRF24
  VDD-DQ-GND
  SDA
  SCL
  GND
  VCC
  1
  2
  3
  I2C
  GN
  3.3V
  IRQ
  MI
  SC
  CE
  MOSI
  CSN
