# Fritzing sketch id4542_TP_001_1 (saved by Fritzing 0.8.7b)

parts:
  Composant1 = LilyPad Arduino USB
  Composant5 = LilyPad LED

nets:
  N1: Composant1.GND, Composant5.-
  N2: Composant1.D10, Composant5.+
