# Fritzing sketch id4542_Wireless_Communication___Transmitter_0 (saved by Fritzing 0.9.3b)
breadboards: 1

parts:
  Part1 = Arduino Uno (Rev3)
  Part2 = NRF24L01+ Breakout Board
  C1 = Capacitor Polarized [package=panasonic_c]
  S1 = Pushbutton [package="[THT]"]
  S2 = Pushbutton [package="[THT]"]
  S3 = Pushbutton [package="[THT]"]
  S4 = Pushbutton [package="[THT]"]
  R1 = Resistor [tolerance=±5% resistance=220 package=THT]
  R2 = Resistor [tolerance=±5% resistance=220 package=THT]
  R3 = Resistor [tolerance=±5% resistance=220 package=THT]
  R4 = Resistor [tolerance=±5% resistance=220 package=THT]

nets:
  N1: Part1.D9_PWM, Part2.CE
  N2: Part1.D10_PWM/SS, Part2.CS
  N3: Part1.D11_PWM/MOSI, Part2.MOSI
  N4: Part1.D12/MISO, Part2.MISO
  N5: Part1.D13/SCK, Part2.SCK
  GND: Part1.GND, Part2.GND, R1.Pin_0, R2.Pin_0, R3.Pin_0, R4.Pin_0
  N6: Part1.D4, Part1.D5_PWM, Part1.D6_PWM, Part1.D7, Part1.5V, C1.-, S1.Pin_3, S1.Pin_4, S2.Pin_3, S2.Pin_4, S3.Pin_3, S3.Pin_4, S4.Pin_3, S4.Pin_4, R1.Pin_1, R2.Pin_1, R3.Pin_1, R4.Pin_1
  3V3: Part1.3V3, Part2.VCC
  N7: S1.Pin_1, S1.Pin_2
  N8: S2.Pin_1, S2.Pin_2
  N9: S3.Pin_1, S3.Pin_2
  N10: S4.Pin_1, S4.Pin_2
