# Fritzing sketch id4544_Door_Sensor_0 (saved by Fritzing 0.9.2b)
circuit board: 4.3cm x 3.15cm
breadboards: 1

parts:
  RFM = RFM12b HopeRF Transceiver [part_number=RFM12B]
  BAT = DC Power [voltage=4.5V part_number="3 x CR44"]
  U1 = ATmega328 [part_number=ATmega328P-AU package=tqfp]
  S1 = SWITCH-MOMENTARY-2 [package=reed_switch_pth]
  R2 = Resistor [tolerance=±5% resistance=10k package="0603 [SMD]"]
  R1 = Resistor [tolerance=±5% resistance=1M package="0603 [SMD]"]
  J2 = male pin header, 2 pins [form="♂ (male)"]
  U2 = Resonator [part_number="CSTCE16M0V53-R0 16MHz" package=resonator-smd]
  C2 = Ceramic Capacitor [capacitance=100nF package="0603 [SMD, multilayer]"]
  U3 = V_REG MIC5219 [part_number=TPS78233DDC package=sot23-5]
  C4 = Ceramic Capacitor [capacitance=4.7µF package="0603 [SMD, multilayer]"]
  C5 = Ceramic Capacitor [capacitance=4.7µF package="0603 [SMD, multilayer]"]
  ANT = Antenna
  C6 = Ceramic Capacitor [capacitance=100nF package="0603 [SMD, multilayer]"]
  R3 = Resistor [tolerance=±5% resistance=1k package="0603 [SMD]"]
  LED = smd LED [color="Red (633nm)" part_number="LS L29K-G1J2-1-Z" package="0603 [SMD]"]
  C1 = Capacitor Polarized [part_number=100µF/16V package=eia7343]
  BAT2 = Pad [width=8 height=8 connect=center]
  BAT3 = Pad [width=8 height=8 connect=center]
  C3 = Ceramic Capacitor [capacitance=100nF package="0603 [SMD, multilayer]"]
  J5 = male pin header, 5 pins [form="♂ (male)" part_number="PROG (0.1in)"]
  BAT1 = Pad [width=8 height=8 connect=center]
  R4 = Resistor [tolerance=±5% resistance=10k package="0603 [SMD]"]
  C7 = Ceramic Capacitor [capacitance=100nF package="0603 [SMD, multilayer]"]
  A2 = Pad [width=1.5 height=1.5 connect=center]
  A0 = Pad [width=1.5 height=1.5 connect=center]
  J1 = male pin header, 2 pins [form="♂ (male)"]
  J3 = male pin header, 2 pins [form="♂ (male)"]
  A1 = Pad [width=1.5 height=1.5 connect=center]  # not connected
  J4 = male pin header, 6 pins [form="♂ (male)"]

nets:
  MISO: RFM.1_SDO, U1.PB4(MISO), J4.pin2
  D2: RFM.2_nIRQ, U1.PD2(INT0)
  N1: RFM.3_FSK/DATA, R2.Pin_1
  GND: RFM.7_GND, RFM.10_GND, BAT.V-, U1.GND, U2.2, C2.0, U3.GND, U3.BP, C4.0, C5.0, C6.0, LED.cathode, C1.-, BAT3.pad, C3.0, J5.pin5, J4.pin6
  N2: RFM.8_ANT, ANT.antenna_lead
  3.3V: RFM.9_VDD, U1.VCC, U1.AVCC, R2.Pin_0, U3.OUT, C5.1, C6.1, C3.1, J5.pin4, R4.Pin_0, J4.pin5
  MOSI: RFM.12_SDI, U1.PB3(MOSI_OC2), J4.pin1
  SCK: RFM.13_SCK, U1.PB5(SCK), J4.pin3
  SS: RFM.14_nSEL, U1.PB2(SS_OC1B)
  N3: BAT.V+, U3.IN, U3.EN, C4.1, C1.+, J1.pin1, J1.pin2
  D3: U1.PD3(INT1), S1.1, R1.Pin_1
  N4: U1.PB6(XTAL1_TOSC1), U2.1
  N5: U1.PB7(XTAL2_TOSC2), U2.3
  N6: U1.PD5(T1), R1.Pin_0
  D8: U1.PB0(ICP), R3.Pin_0
  D9: U1.PB1(OC1A), S1.2
  N7: U1.AREF, C2.1
  A0: U1.PC0(ADC0), A0.pad
  A1: U1.PC1(ADC1)
  A2: U1.PC2(ADC2), A2.pad
  RESET: U1.PC6(_RESET), R4.Pin_1, C7.1, J4.pin4
  N8: U1.PD0(RXD), J5.pin3
  N9: U1.PD1(TXD), J5.pin2
  N10: J2.pin1, J2.pin2, BAT1.pad
  N11: R3.Pin_1, LED.anode
  N12: BAT2.pad, J3.pin1, J3.pin2
  N13: J5.pin1, C7.0

notes:
  A0
  A1
  A2
  BoredomProjects.net
