# Fritzing sketch id4545_GPS_Datalogger_v1_130703_0 (saved by Fritzing 0.7.12b)

parts:
  Wireless_GPS_Datalogger = Arduino Pro Mini 3.3V
  GPS = mystery part, 6 pins [chip_label=GPS]
  SD_Card = mystery part, 7 pins [chip_label="SD Card"]
  Xbee = XBee
  Relay = IC, DIP package, 6 pins [chip_label=Relay]

nets:
  GND: Wireless_GPS_Datalogger.GND, GPS.pin3, SD_Card.pin3, Xbee.GND, Relay.pin2
  N1: Wireless_GPS_Datalogger.VCC, GPS.pin5, SD_Card.pin5, Relay.pin4
  N2: Wireless_GPS_Datalogger.SCK, SD_Card.pin4
  N3: Wireless_GPS_Datalogger.MISO, SD_Card.pin2
  N4: Wireless_GPS_Datalogger.MOSI, SD_Card.pin6
  N5: Wireless_GPS_Datalogger.D10, SD_Card.pin7
  N6: Wireless_GPS_Datalogger.D9, GPS.pin1
  N7: Wireless_GPS_Datalogger.D8, GPS.pin2
  N8: Wireless_GPS_Datalogger.D7, Relay.pin3
  N9: Wireless_GPS_Datalogger.D3, Xbee.pin3
  N10: Wireless_GPS_Datalogger.D2, Xbee.pin2
  N11: GPS.pin4, Xbee.VCC, Relay.pin5
