# Fritzing sketch id4546_fritzing_sketch_2_lights_0 (saved by Fritzing 0.9.0b)
breadboards: 1

parts:
  R1 = Resistor [tolerance=±5% resistance=330 package=THT]
  Part1 = Arduino Uno (Rev3)
  LED1 = LED - 5mm [color="Red (633nm)" package="5 mm [THT]"]
  R2 = Resistor [tolerance=±5% resistance=330 package=THT]
  LED2 = LED - 5mm [color="Blue (430nm)" package="5 mm [THT]"]

nets:
  N1: R1.Pin_0, Part1.D13/SCK
  N2: R1.Pin_1, LED1.anode
  N3: Part1.D12/MISO, R2.Pin_0
  N4: Part1.GND, LED1.cathode, LED2.cathode
  N5: R2.Pin_1, LED2.anode
