# Fritzing sketch id4547_RGB_LED_0 (saved by Fritzing 0.8.7b)
breadboards: 1

parts:
  Часть1 = Arduino Uno (Rev3)
  LED1 = RGB LED (com. anode, rbg) [package="5 mm [THT]"]
  R1 = Resistor [tolerance=±5% resistance=220 package=THT]
  R2 = Resistor [tolerance=±5% resistance=220 package=THT]
  R3 = Resistor [tolerance=±5% resistance=220 package=THT]

nets:
  N1: Часть1.D9_PWM, R3.Pin_0
  N2: Часть1.D10_PWM/SS, R1.Pin_0
  N3: Часть1.D11_PWM/MOSI, R2.Pin_0
  N4: Часть1.GND, LED1.common_anode
  N5: LED1.red_cathode, R2.Pin_1
  N6: LED1.blue_cathode, R1.Pin_1
  N7: LED1.green_cathode, R3.Pin_1
