# Fritzing sketch id4548_Arduino_Schematic_0 (saved by Fritzing 0.9.3b)
breadboards: 1

parts:
  Part1 = Arduino Uno (Rev3)
  R1 = Rotary Potentiometer (Small) [maximum_resistance=100kΩ package=THT]  # not connected
  LCD1 = LCD screen
  R2 = Rotary Potentiometer (Small) [maximum_resistance=100kΩ package=THT]
  VCC1 = Battery
  R3 = Resistor [tolerance=±5% resistance=220 package=THT]

nets:
  N1: Part1.D8, LCD1.E
  N2: Part1.D9_PWM, LCD1.DB4
  N3: Part1.D10_PWM/SS, LCD1.DB6
  N4: Part1.D11_PWM/MOSI, LCD1.DB5
  N5: Part1.D12/MISO, LCD1.DB7
  N6: Part1.GND, VCC1.-
  N7: Part1.D7, LCD1.RS
  N8: Part1.VIN, VCC1.+
  N9: LCD1.VSS, LCD1.R/W, LCD1.LED-
  N10: LCD1.VDD, LCD1.LED+
  N11: R2.leg2, R3.Pin_0
