# Fritzing sketch id4549_16_0 (saved by Fritzing 0.9.3b)
breadboards: 1

parts:
  Part1 = Arduino Uno (Rev3)
  R1 = Resistor [tolerance=±5% resistance=220 package=THT]
  R2 = Resistor [tolerance=±5% resistance=220 package=THT]
  R3 = Resistor [tolerance=±5% resistance=220 package=THT]
  LED1 = RGB LED (com. cathode, rgb) [package="5 mm [THT]"]

nets:
  N1: Part1.D8, R1.Pin_1
  N2: Part1.D10_PWM/SS, R3.Pin_0
  N3: Part1.5V, LED1.common_cathode
  N4: R1.Pin_0, LED1.red_anode
  N5: R2.Pin_1, LED1.green_anode
  N6: R3.Pin_1, LED1.blue_anode
