# Fritzing sketch id454_DMX_Slave_with_Conceptinetics_0 (saved by Fritzing 0.9.2b)
breadboards: 1

parts:
  Bauteil1 = Arduino Nano (Rev3.0)
  U1 = MAX485 [package=dil08]
  XLR1 = XLR3_NCFAH2 [package=xlr3_nc3fah2]

nets:
  N1: Bauteil1.D0/RX, U1.RO
  N2: Bauteil1.GND, U1.RE, U1.DE
  5V: Bauteil1.5V, U1.VCC
  N3: U1.GND, XLR1.1
  N4: U1.A, XLR1.2
  N5: U1.B, XLR1.3
