# Fritzing sketch id4550_wixel_bonsai3_0 (saved by Fritzing 0.8.3b)
circuit board: 5.67cm x 1.77472cm
breadboards: 1

parts:
  J1 = female pin header, 12 pins [form="♀ (female)"]
  J2 = female pin header, 12 pins [form="♀ (female)"]
  TMP36 = TMP36 Temperature Sensor [package="TO92 [THT]"]
  LTC = dps
  L1 = Inductor [inductance=6.8µH package="0805 [SMD]"]
  C1 = Ceramic Capacitor [capacitance=1µF package="0603 [SMD, multilayer]"]
  R1 = Resistor [tolerance=±5% resistance=10k package="0805 [SMD]"]
  R3 = Resistor [tolerance=±5% resistance=100k package="0805 [SMD]"]
  R2 = Resistor [tolerance=±5% resistance=100 package="0805 [SMD]"]
  U2 = Battery Holders [package=battery-aa]
  SOIL_PROBE = screw terminal, 2 pins
  LDR = Photocell (LDR) [package=THT]
  C2 = Ceramic Capacitor [capacitance=10µF package="0603 [SMD, multilayer]"]

nets:
  GND_1: J1.pin1
  P1_0/SR_P0: J1.pin2, R2.Pin_0
  P1_1: J1.pin3
  P1_2: J1.pin4
  P1_3: J1.pin5
  P1_4: J1.pin6
  P1_5: J1.pin7
  P1_6: J1.pin8
  P1_7: J1.pin9
  nRESET: J1.pin10
  V33: J1.pin11
  GND_2: J1.pin12
  GND/GND_3: J2.pin1, TMP36.GND, LTC.connector1, LTC.connector4, C1.0, U2.-, LDR.pin_1, C2.1
  VIN: J2.pin2, LTC.connector3, C2.0
  VALT: J2.pin3
  P0_0/SR_IL: J2.pin4, R1.Pin_1, LDR.pin_0
  P0_1/SR_IS: J2.pin5, R2.Pin_1, SOIL_PROBE.pin1
  P0_2/SR_V: J2.pin6, TMP36.+Vs, R1.Pin_0
  P0_3: J2.pin7
  P0_4/SR_IT: J2.pin8, TMP36.Vout
  P0_5/SR_P1: J2.pin9, R3.Pin_1
  P2_1: J2.pin10
  P2_2: J2.pin11
  N1: LTC.connector0, LTC.connector2, L1.pin_0, C1.1, U2.+
  N2: LTC.connector5, L1.pin_1
  N3: R3.Pin_0, SOIL_PROBE.pin2

notes:
  wixel_bonsai
