# Fritzing sketch id4552_boardPrinterWodka_0 (saved by Fritzing 0.9.0b)
circuit board: 6.88566cm x 5.36311cm

parts:
  U1 = MMA_ACCEL_CONNECTOR [package=1x08]
  U2 = MMA_ACCEL_CONNECTOR [package=1x08]
  Composant1 = Arduino Uno (Rev3)
  J4 = Basic Servo
  M1 = DC Motor
  J1 = screw terminal, 2 pins
  J3 = screw terminal, 2 pins
  M2 = DC Motor
  J2 = Screw terminal - 2 pins [package=THT]
  RHT1 = Humidity and Temperature Sensor RHT03

nets:
  N1: U1.VCC, Composant1.D9_PWM
  N2: U1.GND, Composant1.D10_PWM/SS
  N3: U1.X, Composant1.D11_PWM/MOSI
  N4: U1.Y, Composant1.D12/MISO
  N5: U1.Z, Composant1.D8
  N6: U1.GS1, Composant1.D7
  N7: U1.GS2, Composant1.D6_PWM
  GND: U1.SLP, U2.GND, Composant1.GND, J4.pulse, RHT1.GND_2
  VCC: U2.VCC, Composant1.5V, J4.vcc, RHT1.Vcc
  N8: U2.X, M1.pin_1, J1.pin2
  N9: U2.Y, M1.pin_2, J1.pin1
  N10: U2.Z, M2.pin_1, J2.pin2
  N11: U2.GS1, M2.pin_2, J2.pin1
  N12: U2.GS2, J3.pin2
  N13: U2.SLP, J3.pin1
  N14: Composant1.D13/SCK, RHT1.Data-signal
  N15: Composant1.D5_PWM, J4.gnd
