# Fritzing sketch id4553_clock_0 (saved by Fritzing 0.9.2b)
breadboards: 2

parts:
  Part1 = Arduino Leonardo (Rev3b)
  IC1 = ULN2003A [package="DIP16 [THT]"]
  HEF1 = HEF4094 [package="DIP16 [THT]"]
  HEF2 = HEF4094 [package="DIP16 [THT]"]
  HEF3 = HEF4094 [package="DIP16 [THT]"]
  HEF4 = HEF4094 [package="DIP16 [THT]"]
  IC2 = ULN2003A [package="DIP16 [THT]"]
  IC3 = ULN2003A [package="DIP16 [THT]"]
  IC4 = ULN2003A [package="DIP16 [THT]"]
  LED1 = LED - 5mm [color="Red (633nm)" package="5 mm [THT]"]
  LED2 = LED - 5mm [color="Red (633nm)" package="5 mm [THT]"]
  Part2 = Real Time Clock Module - DS1307 RTC Breakout Board
  LED3 = LED - 3mm [color="Red (633nm)" package="3 mm [THT]"]
  LED7 = LED - 3mm [color="Red (633nm)" package="3 mm [THT]"]
  LED8 = LED - 3mm [color="Red (633nm)" package="3 mm [THT]"]
  LED9 = LED - 3mm [color="Red (633nm)" package="3 mm [THT]"]
  LED10 = LED - 3mm [color="Red (633nm)" package="3 mm [THT]"]
  LED11 = LED - 3mm [color="Red (633nm)" package="3 mm [THT]"]
  LED12 = LED - 3mm [color="Red (633nm)" package="3 mm [THT]"]
  LED13 = LED - 3mm [color="Red (633nm)" package="3 mm [THT]"]
  LED14 = LED - 3mm [color="Red (633nm)" package="3 mm [THT]"]
  LED15 = LED - 3mm [color="Red (633nm)" package="3 mm [THT]"]
  LED16 = LED - 3mm [color="Red (633nm)" package="3 mm [THT]"]
  LED17 = LED - 3mm [color="Red (633nm)" package="3 mm [THT]"]
  LED18 = LED - 3mm [color="Red (633nm)" package="3 mm [THT]"]
  LED19 = LED - 3mm [color="Red (633nm)" package="3 mm [THT]"]
  LED20 = LED - 3mm [color="Red (633nm)" package="3 mm [THT]"]
  LED21 = LED - 3mm [color="Red (633nm)" package="3 mm [THT]"]
  LED22 = LED - 3mm [color="Red (633nm)" package="3 mm [THT]"]
  LED23 = LED - 3mm [color="Red (633nm)" package="3 mm [THT]"]
  LED24 = LED - 3mm [color="Red (633nm)" package="3 mm [THT]"]
  LED25 = LED - 3mm [color="Red (633nm)" package="3 mm [THT]"]
  LED26 = LED - 3mm [color="Red (633nm)" package="3 mm [THT]"]
  LED27 = LED - 3mm [color="Red (633nm)" package="3 mm [THT]"]
  LED28 = LED - 3mm [color="Red (633nm)" package="3 mm [THT]"]
  LED29 = LED - 3mm [color="Red (633nm)" package="3 mm [THT]"]

nets:
  N1: Part1.D5_PWM, HEF1.OE, HEF2.OE, HEF3.OE, HEF4.OE
  VDD: Part1.5V, HEF1.Vdd, HEF2.Vdd, HEF3.Vdd, HEF4.Vdd, Part2.5V
  VSS: Part1.GND, IC1.0V, HEF1.Vss, HEF2.Vss, HEF3.Vss, HEF4.Vss, IC2.0V, IC3.0V, IC4.0V, LED1.cathode, LED2.cathode, Part2.GND, LED3.cathode, LED7.cathode, LED8.cathode, LED9.cathode, LED10.cathode, LED11.cathode, LED12.cathode, LED13.cathode, LED14.cathode, LED15.cathode, LED16.cathode, LED17.cathode, LED18.cathode, LED19.cathode, LED20.cathode, LED21.cathode, LED22.cathode, LED23.cathode, LED24.cathode, LED25.cathode, LED26.cathode, LED27.cathode, LED28.cathode, LED29.cathode
  N2: Part1.D8/A8, HEF1.CLOCK, HEF1.Qs, HEF2.CLOCK, HEF3.DATA, HEF3.CLOCK, HEF4.CLOCK
  N3: Part1.D9_PWM/A9, HEF4.DATA
  N4: Part1.D10_PWM/A10, HEF1.STROBE, HEF2.STROBE, HEF3.STROBE, HEF3.Q4, HEF4.STROBE
  N5: Part1.SDA, Part2.SDA
  N6: Part1.SCL, Part2.SCL
  N7: IC1.In_1, HEF1.Q1
  N8: IC1.In_2, HEF1.Q2
  N9: IC1.In_3, HEF1.Q3
  N10: IC1.In_4, HEF1.Q4
  N11: IC1.In_5, HEF1.Q5
  N12: IC1.In_6, HEF1.Q6
  N13: IC1.In_7, HEF1.Q7
  N14: IC1.COM_-_Common, LED26.anode
  N15: IC1.Out_7, LED24.anode
  N16: IC1.Out_6, LED25.anode
  N17: IC1.Out_5, LED27.anode
  N18: IC1.Out_4, LED23.anode
  N19: IC1.Out_3, LED28.anode
  N20: IC1.Out_2, LED29.anode
  N21: IC1.Out_1, LED22.anode
  N22: HEF1.DATA, HEF2.Qs
  N23: HEF2.DATA, HEF4.Qs
  N24: HEF2.Q1, IC2.In_1
  N25: HEF2.Q2, IC2.In_2
  N26: HEF2.Q3, IC2.In_3
  N27: HEF2.Q4, IC2.In_4
  N28: HEF2.Q7, IC2.In_7
  N29: HEF2.Q6, IC2.In_6
  N30: HEF2.Q5, IC2.In_5
  N31: HEF3.Q1, IC4.In_1
  N32: HEF3.Q2, IC4.In_2
  N33: HEF4.Q1, IC3.In_1
  N34: HEF4.Q2, IC3.In_2
  N35: HEF4.Q3, IC3.In_3
  N36: HEF4.Q4, IC3.In_4
  N37: HEF4.Q7, IC3.In_7
  N38: HEF4.Q6, IC3.In_6
  N39: HEF4.Q5, IC3.In_5
  N40: IC2.COM_-_Common, LED18.anode
  N41: IC2.Out_7, LED16.anode
  N42: IC2.Out_6, LED17.anode
  N43: IC2.Out_5, LED19.anode
  N44: IC2.Out_4, LED15.anode
  N45: IC2.Out_3, LED20.anode
  N46: IC2.Out_2, LED21.anode
  N47: IC2.Out_1, LED14.anode
  N48: IC3.COM_-_Common, LED13.anode
  N49: IC3.Out_7, LED12.anode
  N50: IC3.Out_6, LED11.anode
  N51: IC3.Out_5, LED10.anode
  N52: IC3.Out_4, LED7.anode
  N53: IC3.Out_3, LED8.anode
  N54: IC3.Out_2, LED9.anode
  N55: IC3.Out_1, LED3.anode
  N56: IC4.Out_2, LED2.anode
  N57: IC4.Out_1, LED1.anode
