# Fritzing sketch id4556_debounce_0 (saved by Fritzing 0.9.2b)
breadboards: 1

parts:
  S1 = Pushbutton [package="[THT]"]
  LED1 = LED - 5mm [color="Red (633nm)" package="5 mm [THT]"]
  R1 = Resistor [tolerance=±5% resistance=220 package=THT]
  R2 = Resistor [tolerance=±5% resistance=10k package=THT]
  Part1 = Arduino Uno (Rev3)

nets:
  N1: S1.Pin_1, S1.Pin_2, R2.Pin_0, Part1.D2
  N2: S1.Pin_3, S1.Pin_4, Part1.5V
  N3: LED1.cathode, R1.Pin_0
  N4: LED1.anode, Part1.D9_PWM
  N5: R1.Pin_1, R2.Pin_1, Part1.GND
