# Fritzing sketch id4557_L298N_Circuit_0 (saved by Fritzing 0.9.1b)

parts:
  Arduino_UNO = Arduino Uno (Rev3)
  L298N = L298_BRIDGE_DRIVER [package=powerso20]
  M1 = DC Motor
  M2 = DC Motor
  VCC1 = Battery
  VCC2 = Battery
  VCC3 = Battery
  VCC4 = Battery

nets:
  N1: Arduino_UNO.D9_PWM, L298N.IN4
  N2: Arduino_UNO.D10_PWM/SS, L298N.ENA
  N3: Arduino_UNO.D11_PWM/MOSI, L298N.ENB
  GND: Arduino_UNO.GND, L298N.GND, VCC4.-
  N4: Arduino_UNO.D3_PWM, L298N.IN1
  N5: Arduino_UNO.D5_PWM, L298N.IN2
  N6: Arduino_UNO.D6_PWM, L298N.IN3
  5V: Arduino_UNO.5V, L298N.VSS
  N7: L298N.OUT1, M2.pin_1
  N8: L298N.OUT2, M2.pin_2
  N9: L298N.VS, VCC1.+
  N10: L298N.OUT3, M1.pin_1
  N11: L298N.OUT4, M1.pin_2
  N12: VCC1.-, VCC2.+
  N13: VCC2.-, VCC3.+
  N14: VCC3.-, VCC4.+
