# Fritzing sketch id4558_esquema_temperatura_e_luz_0 (saved by Fritzing 0.9.3b)
breadboards: 1

parts:
  Part1 = Arduino Uno (Rev3)
  S1 = Pushbutton [package="[THT]"]
  T1 = LM35 Temperature Sensor [package="TO92 [THT]"]
  R1 = Photocell (LDR) [package=THT]
  R2 = Resistor [tolerance=±5% resistance=220 package=THT]
  LED1 = LED - 5mm [color="Red (633nm)" package="5 mm [THT]"]  # not connected
  R3 = Resistor [tolerance=±5% resistance=220 package=THT]
  R4 = Resistor [tolerance=±5% resistance=220 package=THT]
  J1 = Basic Servo

nets:
  N1: Part1.A0, R1.pin_0, R3.Pin_1
  N2: Part1.A1, T1.Vout
  N3: Part1.D2, S1.Pin_3, S1.Pin_4, R4.Pin_1
  N4: Part1.D3_PWM, R2.Pin_1
  N5: Part1.D4, J1.pulse
  5V: Part1.5V, S1.Pin_1, S1.Pin_2, T1.+Vs, R1.pin_1, J1.vcc
  GND: Part1.GND, T1.GND, R3.Pin_0, R4.Pin_0, J1.gnd
