# Fritzing sketch id455_Arduino_Door_Bell_With_Push_Button_And_3_LED_0 (saved by Fritzing 0.9.2b)
breadboards: 1

parts:
  Part1 = Arduino Uno (Rev3)
  J1 = Piezo Speaker
  LED1 = LED - 5mm [color="Red (633nm)" package="5 mm [THT]"]
  LED2 = LED - 5mm [color="Yellow (592nm)" package="5 mm [THT]"]
  LED3 = LED - 5mm [color="Green (565nm)" package="5 mm [THT]"]
  R1 = Resistor [tolerance=±5% resistance=220 package=THT]
  R3 = Resistor [tolerance=±5% resistance=220 package=THT]
  R4 = Resistor [tolerance=±5% resistance=220 package=THT]
  S1 = Pushbutton [package="[THT]"]
  R5 = Resistor [tolerance=±5% resistance=1k package=THT]

nets:
  N1: Part1.D8, J1.pin2
  N2: Part1.D12/MISO, S1.Pin_3, S1.Pin_4, R5.Pin_0
  N3: Part1.D3_PWM, LED1.anode, R1.Pin_0, R1.Pin_1
  N4: Part1.D4, LED2.anode, R4.Pin_0, R4.Pin_1
  N5: Part1.D5_PWM, LED3.anode, R3.Pin_0, R3.Pin_1
  N6: Part1.3V3, S1.Pin_1, S1.Pin_2
  N7: Part1.GND, LED1.cathode, LED2.cathode, LED3.cathode, R5.Pin_1
