# Fritzing sketch id4560_stepper_schematic_detailed_project_design_0 (saved by Fritzing 0.9.3b)
breadboards: 1

parts:
  Part1 = Arduino Nano (Rev3.0)
  IC1 = H-Bridge [package=THT]
  M1 = Stepper Motor - Bipolar
  IC2 = H-Bridge [package=THT]
  M2 = Stepper Motor - Bipolar
  3-Axis_Accelerometer1 = 3-Axis Accelerometer Breakout - MMA8452Q
  Part2 = NRF24L01+ Breakout Board
  BAT1 = Battery Holders [package=battery]
  BAT2 = Battery Holders [package=battery]

nets:
  N1: Part1.D1/TX, Part2.CE
  N2: Part1.D0/RX, Part2.CS
  GND: Part1.GND, IC1.GND1, IC1.GND2, IC1.GND3, IC1.GND4, IC2.GND1, IC2.GND2, IC2.GND3, IC2.GND4, 3-Axis_Accelerometer1.GND, Part2.GND, BAT1.-, BAT2.-
  N3: Part1.D4, IC1.1A
  N4: Part1.D5, IC1.2A
  N5: Part1.D6, IC1.3A
  N6: Part1.D7, IC1.4A
  N7: Part1.D8, IC2.1A
  N8: Part1.D9, IC2.2A
  N9: Part1.D10, IC2.3A
  N10: Part1.D11/MOSI, IC2.4A
  N11: Part1.VIN, BAT2.+
  N12: Part1.5V, IC1.1_2EN, IC1.3_4EN, IC1.VCC1, IC2.1_2EN, IC2.3_4EN, IC2.VCC1
  N13: Part1.A5, 3-Axis_Accelerometer1.SCL
  N14: Part1.A4, 3-Axis_Accelerometer1.SDA
  N15: Part1.A2, 3-Axis_Accelerometer1.I2
  N16: Part1.A1, 3-Axis_Accelerometer1.I1
  3V3: Part1.3V3, 3-Axis_Accelerometer1.3.3V, Part2.VCC
  N17: IC1.1Y, M1.A
  N18: IC1.2Y, M1.C
  N19: IC1.VCC2, IC2.VCC2, BAT1.+
  N20: IC1.3Y, M1.B
  N21: IC1.4Y, M1.D
  N22: IC2.1Y, M2.B
  N23: IC2.2Y, M2.D
  N24: IC2.3Y, M2.A
  N25: IC2.4Y, M2.C
