# Fritzing sketch id4562_weather_with_earthquake_0 (saved by Fritzing 0.9.3b)
breadboards: 1

parts:
  Part1 = Arduino Uno (Rev3)
  U1 = LCD-16X2 [package=lcd-16x2_noholes]
  R1 = Rotary Potentiometer (Large) [maximum_resistance=100kΩ package=THT]
  R2 = Resistor [tolerance=±5% resistance=220 package="0603 [SMD]"]
  RHT1 = Humidity and Temperature Sensor RHT03
  Part2 = Barometric Pressure Sensor - BMP085 Breakout
  Part5 = Triple Axis Accelerometer Breakout - ADXL345
  Part6 = Arduino Cellular Shield

nets:
  N1: Part1.A0, RHT1.Data-signal
  N2: Part1.A4/SDA, Part2.SCL
  N3: Part1.A5/SCL, Part2.SDA
  N4: Part1.D8, Part6.RX-I
  N5: Part1.D9_PWM, Part6.TX-O
  N6: Part1.D10_PWM/SS, Part5.CS
  N7: Part1.D11_PWM/MOSI, Part5.SDA
  N8: Part1.D12/MISO, Part5.SDO
  N9: Part1.D13/SCK, Part5.SCL
  GND: Part1.GND, U1.VSS, U1.R_W, U1.K, R1.leg2, RHT1.GND_2, Part2.XCLR, Part5.GND, Part6.GND
  N10: Part1.D2, U1.DB7
  N11: Part1.D3_PWM, U1.DB6
  N12: Part1.D4, U1.DB5
  N13: Part1.D5_PWM, U1.DB4
  N14: Part1.D6_PWM, U1.E
  N15: Part1.D7, U1.RS
  3V3: Part1.3V3, Part2.EOC, Part5.VCC
  5V: Part1.5V, U1.VDD, R1.leg1, R2.Pin_1, RHT1.Vcc
  N16: U1.VO, R1.wiper
  N17: U1.A, R2.Pin_0
