# Fritzing sketch id4563_sensor_v4_detached_0 (saved by Fritzing 0.7.10b)
breadboards: 1

parts:
  Gnd = male pin header, 1 pin [form="♂ (male)"]
  DHT = AM2302_Humidity_and_Temperature_Sensor
  BMP = BMP085_Breakout
  PR = Photocell (LDR) [package=THT]
  R1 = Resistor [tolerance=±5% resistance=220 package=THT]
  LT = male pin header, 1 pin [form="♂ (male)"]
  SCL = male pin header, 1 pin [form="♂ (male)"]
  SDA = male pin header, 1 pin [form="♂ (male)"]
  HT = male pin header, 1 pin [form="♂ (male)"]
  Vcc = male pin header, 1 pin [form="♂ (male)"]

nets:
  N1: Gnd.pin1, DHT.connector3, BMP.connector7, PR.pin_1
  N2: DHT.connector1, BMP.connector1, R1.Pin_1, Vcc.pin1
  N3: DHT.connector2, HT.pin1
  N4: BMP.connector3, SCL.pin1
  N5: BMP.connector4, SDA.pin1
  N6: PR.pin_0, R1.Pin_0, LT.pin1

notes:
  WSense v1 - 2012
  Gnd
  Data
  Vcc
  Vcc: 3.3 or 5V
  HT : 1-Wire - DHT22
  LT : analogic
  Nicolas Dufour
