# Fritzing sketch id4564_X_Mas_Lily_Pad_0 (saved by Fritzing 0.9.3b)

parts:
  Bauteil1 = Lilypad Arduino Board
  C1 = Electrolytic Capacitor [capacitance=1µF package="100 mil [THT, electrolytic]"]
  BATT1 = LiPoly_Battery__1300mAh
  SPKR1 = Loudspeaker

nets:
  GND: Bauteil1.GND, Bauteil1.D4, BATT1.connector2, SPKR1.pin2
  N1: Bauteil1.VCC, BATT1.connector1
  N2: Bauteil1.D9, C1.+
  N3: C1.-, SPKR1.pin1

notes:
  Press Reset to start the melody!
  After playing the melody processor goes in deep sleep, no extra switch is required!
  Connect it direct to the programmer connection!
  Dont forget to program before
  Until cable is connected each time after you start the melody by pressing reset it will change to another melody!
  Once removed the last played melody will stay!
  Melodies:
  OhTannenbaum
  WeddingMarch
  YankyDoodle
  Fanfare
  laCucaracha
  HappyBirthDay
  AllMyDucks
  JingleBells
  No PCB required
  Just temporary!
