# Fritzing sketch id4565_X_MAS_Melody_0 (saved by Fritzing 0.9.1b)
circuit board: 3.5cm x 1.2cm
breadboards: 1

parts:
  Bauteil1 = Arduino Uno (Rev3)
  SPKR1 = Loudspeaker [part_number="8 Ohm"]
  S1 = Pushbutton [package="[THT]"]
  S2 = Pushbutton [package="[THT]"]
  R1 = Resistor [tolerance=±10% resistance=150 package="1206 [SMD]"]

nets:
  N1: Bauteil1.D9_PWM, SPKR1.pin2
  GND: Bauteil1.GND, S1.Pin_3, S1.Pin_4, S2.Pin_3, S2.Pin_4, R1.Pin_0
  N2: Bauteil1.D2, S2.Pin_1, S2.Pin_2
  N3: Bauteil1.D4, S1.Pin_1, S1.Pin_2
  N4: SPKR1.pin1, R1.Pin_1

notes:
  Start to play melody
  Keep pressed when pressing start at the sametime and melody will change.
  Keep S1 pressed when pressing start S2 at the sametime and melody will change.
  S2 Start to play melody
