# Fritzing sketch id4566_XbeeBO_0 (saved by Fritzing 0.8.7b)
circuit board: 3.00566cm x 3.62656cm
breadboards: 1

parts:
  DTR = Header 1 [package=1x01_offset]  # not connected
  3_3V = Header 1 [package=1x01_offset]
  GND = Header 1 [package=1x01_offset]  # not connected
  RSSI = Header 1 [package=1x01_offset]
  RST = Header 1 [package=1x01_offset]
  RX = Header 1 [package=1x01_offset]
  TX = Header 1 [package=1x01_offset]
  RTS = Header 1 [package=1x01_offset]  # not connected
  ASS = Header 1 [package=1x01_offset]  # not connected
  CTS = Header 1 [package=1x01_offset]  # not connected
  U1 = XBEE-1 [package=xbee-smd]
  U2 = mystery part, 11 pins [chip_label=?]
  SLP = Header 1 [package=1x01_offset]

nets:
  N1: 3_3V.1, U1.VDD
  N2: RSSI.1, U1.RSSI
  N3: RST.1, U1.RESET
  N4: RX.1, U1.DIN
  N5: TX.1, U1.DOUT
  N6: U1.DTR, U2.pin10
  N7: U1.GND, U2.pin9
  N8: U1.CTS, U2.pin2
  N9: U1.DIO9, SLP.1
  N10: U1.DIO5, U2.pin3
  N11: U1.RTS, U2.pin4

notes:
  Made With Fritzing
