# Fritzing sketch id4567_Button_And_Temp_0 (saved by Fritzing 0.8.7b)
breadboards: 1

parts:
  U1 = XBee
  T1 = LM35 Temperature Sensor [package="TO92 [THT]"]
  S1 = Round Pushbutton

nets:
  N1: U1.connector0, T1.+Vs
  N2: U1.connector8, U1.connector19, T1.GND, S1.leg1
  N3: U1.connector9, S1.leg0
  N4: U1.connector18, T1.Vout

notes:
  + 3.3 V
  Ground
  PIN 10
  PIN 1
  PIN 9
  PIN 11
  PIN 12
  Pin 1 = +3.3 V
  Pin 9 = Sleep / ON
  Pin 10 = Ground
  Pin 11 = digital input
  Pin 12 = analogic input
  LM 35
  analogic temperature probe
