# Fritzing sketch id4568_XBeeEmonSensor85_1.0_0 (saved by Fritzing 0.8.3b)
circuit board: 5.72908cm x 2.67641cm
breadboards: 1

parts:
  Attiny85 = attiny85 [package=dip]
  Actv = LED - 3mm [color="Red (633nm)" package="3 mm [THT]"]
  RSSI = LED - 3mm [color="Red (633nm)" package="3 mm [THT]"]
  Assc = LED - 3mm [color="Red (633nm)" package="3 mm [THT]"]
  XBee = XBee
  + = female pin header, 1 pin [form="♀ (female)"]
  - = female pin header, 1 pin [form="♀ (female)"]  # not connected
  220 = Resistor [tolerance=±5% resistance=220 package=THT]
  220_2 = Resistor [tolerance=±5% resistance=220 package=THT]
  220_3 = Resistor [tolerance=±5% resistance=220 package=THT]
  10K = Resistor [tolerance=±5% resistance=220 package=THT]
  10K_2 = Resistor [tolerance=±5% resistance=220 package=THT]
  10uf = Electrolytic Capacitor [capacitance=1µF package="100 mil [THT, electrolytic]"]
  TRS1 = Audio Jack (TRS) 3.5mm [package="PG203J [THT]"]

nets:
  N1: Attiny85.Pin_2, XBee.pin2
  N2: Attiny85.Pin_3, XBee.pin3
  N3: Attiny85.Pin_5, 220_3.Pin_1, 10K.Pin_0
  N4: Attiny85.Pin_6, XBee.pin9
  N5: Attiny85.Pin_7, 10K.Pin_1, 10K_2.Pin_1, 10uf.+, TRS1.Tip
  N6: Attiny85.Pin_8, XBee.VCC, +.pin1
  N7: Actv.anode, 220_3.Pin_0
  N8: RSSI.anode, 220_2.Pin_1
  N9: Assc.anode, 220.Pin_0
  N10: XBee.pin6, 220_2.Pin_0
  N11: XBee.pin15, 220.Pin_1

notes:
  exsertus.com
  XBeeEMONSensor85 v1.0
