# Fritzing sketch id456_Doorbell_0 (saved by Fritzing 0.7.10b)
breadboards: 1

parts:
  U1 = Arduino Mega
  J1 = Piezo Speaker
  S1 = Pushbutton [package=THT]
  R1 = Resistor [tolerance=±5% resistance=10k package=THT]

nets:
  N1: U1.GND, J1.pin1, R1.Pin_1
  N2: U1.D8, J1.pin2
  N3: U1.D2, S1.leg0, R1.Pin_0
  N4: U1.+5V, S1.leg1
