# Fritzing sketch id4570_XBeeSensor85_1.2_0 (saved by Fritzing 0.8.3b)
circuit board: 5.26811cm x 3.09268cm
breadboards: 1

parts:
  Attiny85 = attiny85 [package=dip]
  Sensor = female pin header, 3 pins [form="♀ (female)"]
  Actv = LED - 3mm [color="Red (633nm)" package="3 mm [THT]"]
  RSSI = LED - 3mm [color="Red (633nm)" package="3 mm [THT]"]
  Assc = LED - 3mm [color="Red (633nm)" package="3 mm [THT]"]
  XBee = XBee
  3V3_Reg = female pin header, 3 pins [form="♀ (female)"]
  + = Battery
  +_2 = female pin header, 1 pin [form="♀ (female)"]
  - = female pin header, 1 pin [form="♀ (female)"]  # not connected
  220 = Resistor [tolerance=±5% resistance=220 package=THT]
  220_2 = Resistor [tolerance=±5% resistance=220 package=THT]
  220_3 = Resistor [tolerance=±5% resistance=220 package=THT]

nets:
  N1: Attiny85.Pin_2, XBee.pin2
  N2: Attiny85.Pin_3, XBee.pin3
  N3: Attiny85.Pin_5, Sensor.pin2, 220_3.Pin_0
  N4: Attiny85.Pin_6, XBee.pin9
  N5: Attiny85.Pin_7, Sensor.pin3
  N6: Attiny85.Pin_8, XBee.VCC, 3V3_Reg.pin2
  N7: Actv.anode, 220_3.Pin_1
  N8: RSSI.anode, 220_2.Pin_1
  N9: Assc.anode, 220.Pin_0
  N10: XBee.pin6, 220_2.Pin_0
  N11: XBee.pin15, 220.Pin_1
  N12: 3V3_Reg.pin3, +.+, +_2.pin1

notes:
  exsertus.com
  XBeeSensor85 v1.2
  -
  Vcc
  3v3
  Gnd
