# Fritzing sketch id4570_shy_dildo (saved by Fritzing 0.5.2b)
breadboards: 1

parts:
  U1 = 555 Timer [package="DIP8 [THT]"]
  U2 = Voltage Regulator - 5V [package="TO220 [THT]"]
  part = IC, DIP package, 6 pins [chip_label=IQS127 spacing=300mil]
  1_25_V_Motor = DC Motor
  1N4148 = Rectifier Diode [package="300 mil [THT]"]
  Power_plug1 = Power plug
  10µF = Electrolytic Capacitor [capacitance=56µF rated_voltage=35V package="100 mil [THT, electrolytic]"]
  0_1µF = Ceramic Capacitor [capacitance=100nF rated_voltage=35V package="100 mil [THT, multilayer]"]
  50µF = Electrolytic Capacitor [capacitance=100nF rated_voltage=35V package="100 mil [THT, electrolytic]"]
  0_1µF_2 = Ceramic Capacitor [capacitance=100nF rated_voltage=35V package="100 mil [THT, multilayer]"]
  MPSU45 = npn-Powertransistor [package="TO220 [THT]"]
  Proximity/Touch_Pad = Pushbutton [package=THT]
  1µF = Ceramic Capacitor [capacitance=100nF rated_voltage=35V package="100 mil [THT, multilayer]"]
  1µF_2 = Ceramic Capacitor [capacitance=100nF rated_voltage=35V package="100 mil [THT, multilayer]"]
  1_2k = Resistor [resistance=220 package=THT]
  2_2µF = Tantalum Capacitor [capacitance=100nF rated_voltage=35V package="100 mil [THT, tantalum]"]
  4_7k = Resistor [resistance=220 package=THT]
  0_1µF_3 = Ceramic Capacitor [capacitance=100nF rated_voltage=35V package="100 mil [THT, multilayer]"]
  10k = Resistor [resistance=220 package=THT]
  1N4001 = Rectifier Diode [package="300 mil [THT]"]
  1N4001_2 = Rectifier Diode [package="300 mil [THT]"]

nets:
  GND: U1.Ground, U2.GND, part.pin2, Power_plug1.GND, 10µF.-, 0_1µF.0, 50µF.-, 0_1µF_2.0, MPSU45.emitter, 1µF.0, 1µF_2.0, 2_2µF.-, 0_1µF_3.0, 1N4001.anode
  N1: U1.Trigger, U1.Threshold, 1N4148.cathode, 2_2µF.+, 4_7k.Pin_1
  N2: U1.Output, 10k.Pin_1
  N3: U1.Reset, part.pin1
  N4: U1.Control_Voltage, 0_1µF_3.1
  N5: U1.Discharge, 1N4148.anode, 1_2k.Pin_1, 4_7k.Pin_0
  5V: U1.Vcc_Supply_Voltage, U2.output_voltage, part.pin5, 1_25_V_Motor.pin_2, 10µF.+, 0_1µF.1, 1µF.1, 1_2k.Pin_0, 1N4001_2.cathode
  N6: U2.input_voltage, Power_plug1.VCC, 50µF.+, 0_1µF_2.1
  N7: part.pin4, 1µF_2.1
  N8: part.pin6, Proximity/Touch_Pad.leg1
  N9: 1_25_V_Motor.pin_1, MPSU45.collector, 1N4001.cathode, 1N4001_2.anode
  N10: MPSU45.base, 10k.Pin_0
