# Fritzing sketch id4571_xbee_test_0 (saved by Fritzing 0.9.3b)
circuit board: 10cm x 6cm
breadboards: 1

parts:
  Componente1 = Arduino Mega 2560 (Rev3)
  Componente3 = XBee Explorer Regulated  # not connected
  Componente4 = XBee Explorer Regulated
  Componente5 = Triple Axis Magnetometer - HMC5883 Breakout
  U3 = Mini-USB _B_ connector with 5th pin broken out. [package=usb-minib]  # not connected

nets:
  N1: Componente1.D21/SCL, Componente1.SCL, Componente5.SCL
  N2: Componente1.D20/SDA, Componente1.SDA, Componente5.SDA
  N3: Componente1.D19/RX1, Componente4.DOUT
  N4: Componente1.D18/TX1, Componente4.DIN
  GND: Componente1.GND, Componente4.GND, Componente5.GND
  5V: Componente1.5V, Componente4.5V, Componente5.VCC
