# Fritzing sketch id4572_XBee_Arduino_mini_v02_0 (saved by Fritzing 0.8.7b)
circuit board: 3.05773cm x 3.01654cm
breadboards: 1

parts:
  R2 = Resistor [tolerance=±5% resistance=68 package="1206 [SMD]"]
  S1 = SWITCH-MOMENTARY-2 [package=tactile_switch_smd-2]
  R3 = Resistor [tolerance=±5% resistance=10k package="1206 [SMD]"]
  C4 = Ceramic Capacitor [capacitance=0.1µF package="1206 [SMD, multilayer]"]
  part = FTDI_BASIC [package=ftdi_basic]
  C6 = Ceramic Capacitor [capacitance=0.1µF package="1206 [SMD, multilayer]"]
  part_2 = female pin header, 8 pins [form="♀ (female)"]
  part_3 = female pin header, 8 pins [form="♀ (female)"]
  part_4 = female pin header, 8 pins [form="♀ (female)"]
  part_5 = female pin header, 8 pins [form="♀ (female)"]
  part_6 = XBEE-1 [package=xbee-1]
  IC = ATmega328 [package=tqfp]
  C1 = Capacitor Polarized [package=eia3216]
  C2 = Capacitor Polarized [package=eia3216]
  LED1 = smd LED [color="Red (633nm)" package="1206 [SMD]"]
  U1 = Voltage Regulator LDO [package=sot23-5]
  Y1 = Resonator [package=resonator-smd]
  part_7 = female pin header, 10 pins [form="♀ (female)"]
  part_8 = female pin header, 10 pins [form="♀ (female)"]
  C5 = Ceramic Capacitor [capacitance=0.1µF package="1206 [SMD, multilayer]"]
  part_9 = female pin header, 2 pins [form="♀ (female)"]

nets:
  3.3V: R2.Pin_0, R3.Pin_1, part.3, part_4.pin2, part_5.pin3, part_5.pin5, part_6.VDD, IC.VCC, IC.AVCC, C2.+, U1.OUT, part_8.pin10, C5.1
  N1: R2.Pin_1, LED1.anode
  N2: S1.2, R3.Pin_0, C4.0, part_3.pin5, IC.PC6(_RESET)
  GND: S1.1, part.1, part.2, C6.1, part_4.pin5, part_5.pin2, part_5.pin4, part_5.pin6, part_6.GND, IC.GND, IC.AGND, C1.-, C2.-, LED1.cathode, U1.GND, Y1.2, part_8.pin1, C5.0, part_9.pin2
  N3: C4.1, part.6
  N4: part.5, part_3.pin7, IC.PD1(TXD)
  N5: part.4, part_3.pin6, IC.PD0(RXD)
  N6: C6.0, part_4.pin4, IC.AREF
  N7: part_2.pin1, IC.PB4(MISO)
  N8: part_2.pin2, IC.PB3(MOSI_OC2)
  N9: part_2.pin3, IC.PB2(SS_OC1B)
  N10: part_2.pin4, IC.PB1(OC1A)
  N11: part_2.pin5, IC.PB0(ICP)
  N12: part_2.pin6, IC.PD7(AIN1)
  N13: part_2.pin7, IC.PD6(AIN0)
  N14: part_2.pin8, IC.PD5(T1)
  N15: part_3.pin1, IC.PC2(ADC2)
  N16: part_3.pin2, IC.PC3(ADC3)
  N17: part_3.pin3, IC.PC4(ADC4_SDA)
  N18: part_3.pin4, IC.PC5(ADC5_SCL)
  N19: part_3.pin8, IC.PD2(INT0)
  N20: part_4.pin1, IC.PB5(SCK)
  N21: part_4.pin3, IC.ADC6
  N22: part_4.pin6, IC.ADC7
  N23: part_4.pin7, IC.PC0(ADC0)
  N24: part_4.pin8, IC.PC1(ADC1)
  N25: part_5.pin7, IC.PD4(XCK_T0)
  N26: part_5.pin8, IC.PD3(INT1)
  N27: part_6.DOUT, part_8.pin9
  N28: part_6.DIN, part_8.pin8
  N29: part_6.DIO12, part_8.pin7
  N30: part_6.RESET, part_8.pin6
  N31: part_6.RSSI, part_8.pin5
  N32: part_6.DIO11, part_8.pin4
  N33: part_6.RES, part_7.pin4, part_8.pin3
  N34: part_6.DTR, part_8.pin2
  N35: part_6.DIO4, part_7.pin1
  N36: part_6.CTS, part_7.pin2
  N37: part_6.DIO9, part_7.pin3
  N38: part_6.DIO5, part_7.pin5
  N39: part_6.RTS, part_7.pin6
  N40: part_6.DIO3, part_7.pin7
  N41: part_6.DIO2, part_7.pin8
  N42: part_6.DIO1, part_7.pin9
  N43: part_6.DIO0, part_7.pin10
  N44: IC.PB6(XTAL1_TOSC1), Y1.1
  N45: IC.PB7(XTAL2_TOSC2), Y1.3
  5V: C1.+, U1.IN, U1.EN, part_9.pin1

notes:
  -
  +
