# Fritzing sketch id4573_XBee+Servo+SPI_Shield_0 (saved by Fritzing 0.7.0b)
breadboards: 1

parts:
  Netduino1 = Netduino
  XBee1 = XBee
  Servo1 = Basic Servo
  Servo2 = Basic Servo
  Servo3 = Basic Servo
  Servo4 = Basic Servo
  SPI1 = female pin header, 6 pins [form="♀ (female)"]
  Pwr = LED - 5mm [color="Red (633nm)" package="5 mm [THT]"]
  R1 = Resistor [tolerance=±5% resistance=220 package=THT]
  Reset = Pushbutton [package="[THT]"]

nets:
  N1: Netduino1.D13_SPCK, SPI1.pin5
  N2: Netduino1.D12_MISO, SPI1.pin4
  N3: Netduino1.D11_MOSI, SPI1.pin3
  N4: Netduino1.D10_PWM3, Servo1.pulse
  N5: Netduino1.D9_PWM2, Servo2.pulse
  N6: Netduino1.D8_CTS1, SPI1.pin2
  N7: Netduino1.D6_PWM1, Servo3.pulse
  N8: Netduino1.D5_PWM0, Servo4.pulse
  N9: Netduino1.D1_TX0, XBee1.pin3
  N10: Netduino1.D0_RX0, XBee1.pin2
  N11: Netduino1.RST, Reset.Pin_1, Reset.Pin_2
  3V3: Netduino1.3V3, XBee1.VCC, SPI1.pin6, Pwr.anode
  GND: Netduino1.GND, XBee1.GND, Servo1.gnd, Servo2.gnd, Servo3.gnd, Servo4.gnd, SPI1.pin1, R1.Pin_0, Reset.Pin_3, Reset.Pin_4
  VCC: Netduino1.VIN, Servo1.vcc, Servo2.vcc, Servo3.vcc, Servo4.vcc
  N12: Pwr.cathode, R1.Pin_1

notes:
  StefansKits.eu
  XBee+Servo+SPI Shield
