# Fritzing sketch id4575_Traffic_lights (saved by Fritzing 0.4.3b)
breadboards: 1

parts:
  LED1 = green LED - 5mm
  LED2 = Red LED - 5mm
  LED3 = Red LED - 5mm  # not connected
  LED4 = green LED - 5mm
  LED5 = yellow LED - 5mm  # not connected
  LED6 = green LED - 5mm
  R1 = Resistor [resistance=470 package=THT]
  Arduino1 = Arduino

nets:
  N1: LED1.cathode, LED2.anode, LED4.anode, LED6.cathode, R1.Pin_1
  N2: LED1.anode, LED2.cathode
  N3: LED4.cathode, Arduino1.D11
  N4: LED6.anode, Arduino1.D12
  N5: R1.Pin_0, Arduino1.GND

notes:
  May be replaced with bi-color led. 2-lead ones work.
