# Fritzing sketch id4576_THEREALBOX (saved by Fritzing 0.9.3b)
breadboards: 1

parts:
  Part1 = Arduino Uno (Rev3) - ICSP
  RHT1 = Humidity and Temperature Sensor RHT03
  LED1 = smd LED [color="Red (633nm)" package="0805 [SMD]"]
  LCD1 = LCD screen
  R1 = TRIMPOT [package=trim_pot_pth]
  U1 = POT [package=pot_mammoth]
  U2 = RELAY [package=relay-jzc]
  M1 = DC Motor
  VCC1 = Battery block 9V  # not connected
  R2 = Resistor [tolerance=±5% resistance=220 package=THT]

nets:
  N1: Part1.A0, U1.A
  N2: Part1.ICSP_MOSI, Part1.D11_PWM/MOSI, LCD1.DB6
  N3: Part1.D8, LCD1.E
  N4: Part1.D9_PWM, LCD1.DB4
  N5: Part1.D10_PWM/SS, LCD1.DB5
  N6: Part1.D12/MISO, LCD1.DB7
  N7: Part1.D2, RHT1.Data-signal
  N8: Part1.D3_PWM, U2.COIL1
  N9: Part1.D5_PWM, LED1.anode
  N10: Part1.D7, LCD1.RS
  5V: Part1.5V, RHT1.Vcc, LCD1.VDD, LCD1.LED+, R1.CCW, U1.S
  GND: Part1.GND, RHT1.GND_1, RHT1.GND_2, LCD1.VSS, LCD1.LED-, R1.CW, U1.E, U2.COIL2, R2.Pin_0
  N11: LED1.cathode, R2.Pin_1
  N12: LCD1.V0, R1.WIPER
  N13: U2.NO, M1.pin_1

notes:
  12V TRANSFO
  12V runs fan
  12V runs Arduino
  Potentiometer used to change TMax
