# Fritzing sketch id4577_Arduino_Based_Robotic_Arm_Control1__0 (saved by Fritzing 0.9.3b)
perfboards: 3

parts:
  Part1 = Arduino Uno (Rev3)  # not connected
  Part2 = Bluetooth HC-05 Macho  # not connected
  M1 = DC Motor  # not connected
  M2 = DC Motor  # not connected
  M3 = DC Motor  # not connected
  M4 = DC Motor  # not connected
  IC1 = L293D [package=THT]  # not connected
  IC2 = L293D [package=THT]  # not connected
  7805 = Capacitor Polarized [package=cpol-radial-1000uf-25v]
  JP1 = Header 2 [package=molex-1x2_lock]  # not connected
  S1 = Toggle Switch [package=THT]  # not connected
  part = LIPO-1000mAh [package=lipo-1000]  # not connected
  R1 = Resistor [tolerance=±5% resistance=220 package="0402 [SMD]"]  # not connected
  LED1 = LED - 5mm [color="Red (633nm)" package="5 mm [THT]"]  # not connected
  IC3 = Voltage Regulator [package=78xxl]  # not connected
  IC4 = Voltage Regulator [package=78xxl]
  JP2 = Header 2 [package=molex-1x2_lock]  # not connected
  JP3 = Header 2 [package=molex-1x2_lock]  # not connected
  JP4 = Header 2 [package=molex-1x2_lock]  # not connected
  JP5 = Header 2 [package=molex-1x2_lock]  # not connected
  JP6 = Header 2 [package=molex-1x2_lock]  # not connected
  JP7 = Header 2 [package=molex-1x2_lock]  # not connected
  JP8 = Header 2 [package=molex-1x2_lock]  # not connected
  H1 = polarizedheader 4pin 0.156in [package=THT]
  H2 = polarizedheader 4pin 0.156in [package=THT]
  H3 = polarizedheader 4pin 0.156in [package=THT]
  H4 = polarizedheader 4pin 0.156in [package=THT]
  JP9 = Header 2 [package=molex-1x2_lock]  # not connected
  JP10 = Header 2 [package=molex-1x2_lock]  # not connected
  JP11 = Header 2 [package=molex-1x2_lock]  # not connected
  U1 = Sharp PC817 [package=THT]  # not connected

nets:
  N1: 7805.+, IC4.IN
  N2: H1.pin3, H1.pin4
  N3: H2.pin3, H2.pin4
  N4: H3.pin3, H3.pin4
  N5: H4.pin3, H4.pin4
