# Fritzing sketch id4579_Untitled_Sketch_0 (saved by Fritzing 0.9.3b)
breadboards: 1

parts:
  S2 = SWITCH-SPST-2 [package=switch-spst-vertical]
  Part1 = Arduino Uno (Rev3) - ICSP
  LED1 = LED - 5mm [color="White (4500K)" package="5 mm [THT]"]
  LED2 = LED - 5mm [color="White (4500K)" package="5 mm [THT]"]
  S3 = SWITCH-SPST-2 [package=switch-spst-vertical]
  LED4 = LED - 5mm [color="White (4500K)" package="5 mm [THT]"]
  LED5 = LED - 5mm [color="White (4500K)" package="5 mm [THT]"]
  S4 = SWITCH-SPST-2 [package=switch-spst-vertical]
  S5 = Pushbutton [package="[THT]"]
  U1 = SWITCH-SPST-2 [package=r_sw_th]
  M1 = DC Motor

nets:
  N1: S2.O, LED1.anode
  N2: S2.P, Part1.D10_PWM/SS
  N3: Part1.GND, LED2.cathode, LED4.cathode, LED5.cathode, M1.pin_2
  N4: Part1.D8, U1.O
  N5: Part1.D9_PWM, S4.P
  N6: LED1.cathode, LED2.anode
  N7: S3.O, LED4.anode
  N8: S3.P, LED5.anode, S4.O
  N9: S5.Pin_1, U1.P
  N10: S5.Pin_3, M1.pin_1
