# Fritzing sketch id457_A4988_Arduino_Nano_0 (saved by Fritzing 0.9.2b)
breadboards: 1

parts:
  MD09B1 = A4988 Stepper Motor Driver Carrier
  Componente1 = Arduino Nano (Rev3.0) (ICSP)
  M1 = Stepper Motor - Unipolar
  Power_Pug_5V = Power plug
  Power_Plug_12V = Power plug
  C2_10_uF = Electrolytic Capacitor [capacitance=1µF package="100 mil [THT, electrolytic]"]
  C1_100uF = Electrolytic Capacitor [capacitance=1µF package="100 mil [THT, electrolytic]"]

nets:
  N1: MD09B1.Enable, Componente1.D7
  N2: MD09B1.MS1, Componente1.D4
  N3: MD09B1.MS2, Componente1.D5
  N4: MD09B1.MS3, Componente1.D6
  N5: MD09B1.RESET, Componente1.D8
  N6: MD09B1.SLEEP, Componente1.D9
  N7: MD09B1.STEP, Componente1.D2
  N8: MD09B1.DIR, Componente1.D3
  N9: MD09B1.VMOT, Power_Plug_12V.VCC, C1_100uF.+
  N10: MD09B1.GROUND#141, Power_Plug_12V.GND, C1_100uF.-
  N11: MD09B1.OUT_2B, M1.A
  N12: MD09B1.OUT_2A, M1.C
  N13: MD09B1.OUT_1A, M1.B
  N14: MD09B1.OUT_1B, M1.D
  VDD: MD09B1.VDD, Componente1.5V, Power_Pug_5V.VCC, C2_10_uF.+
  GND: MD09B1.GROUND#147, Componente1.GND, Power_Pug_5V.GND, C2_10_uF.-
