# Fritzing sketch id4580_lcd_i2c_(1)_0 (saved by Fritzing 0.9.1b)
breadboards: 1

parts:
  Z-uno_2_1 = zuno2
  DS1 = DS18B20 1-Wire Temperature Sensor [part_number=DS18B20]
  R1 = Resistor [tolerance=±5% resistance=220 package=THT]
  VCC1 = 4 x AAA Battery Mount
  U4 = LCD-16X2 [package=lcd-16x2_noholes]  # not connected

nets:
  N1: Z-uno_2_1.connector2, DS1.GND, R1.Pin_0
  N2: Z-uno_2_1.connector3, DS1.VDD, VCC1.-
  N3: Z-uno_2_1.connector15, Z-uno_2_1.connector16
  N4: Z-uno_2_1.connector17, Z-uno_2_1.connector18
  N5: Z-uno_2_1.connector20, DS1.DQ, R1.Pin_1
  N6: Z-uno_2_1.connector41, Z-uno_2_1.connector44
  N7: Z-uno_2_1.connector42, Z-uno_2_1.connector43
