# Fritzing sketch id4582_Z_Uno_HC_SR04_0 (saved by Fritzing 0.9.2b)
breadboards: 1

parts:
  Z-uno_2_1 = zuno2
  Часть1 = SRF05 Ultrasonic Rangefinder
  R1 = Resistor [tolerance=±5% resistance=2.2k package=THT]
  R2 = Resistor [tolerance=±5% resistance=22 package=THT]

nets:
  N1: Z-uno_2_1.connector2, Часть1.connector8
  N2: Z-uno_2_1.connector3, Часть1.connector11, R1.Pin_0
  N3: Z-uno_2_1.connector15, Z-uno_2_1.connector16
  N4: Z-uno_2_1.connector17, Z-uno_2_1.connector18, R1.Pin_1, R2.Pin_1
  N5: Z-uno_2_1.connector19, Часть1.connector9
  N6: Z-uno_2_1.connector41, Z-uno_2_1.connector44
  N7: Z-uno_2_1.connector42, Z-uno_2_1.connector43
  N8: Часть1.connector10, R2.Pin_0
