# Fritzing sketch id4583_Z_Wave_Z_Uno_DHT11_0 (saved by Fritzing 0.9.1b)
breadboards: 1

parts:
  Z-uno_2_1 = zuno2
  DHT1 = DHT11_Temperature_and_Humitidy_Sensor
  R1 = Resistor [tolerance=±5% resistance=10k package=THT]

nets:
  N1: Z-uno_2_1.connector2, DHT1.connector1, R1.Pin_1
  N2: Z-uno_2_1.connector3, DHT1.connector4
  N3: Z-uno_2_1.connector15, Z-uno_2_1.connector16
  N4: Z-uno_2_1.connector17, Z-uno_2_1.connector18, DHT1.connector3
  N5: Z-uno_2_1.connector41, Z-uno_2_1.connector44
  N6: Z-uno_2_1.connector42, Z-uno_2_1.connector43
  N7: DHT1.connector2, R1.Pin_0
