# Fritzing sketch id4584_Z_Wave_Z_Uno_bh1750_0 (saved by Fritzing 0.9.2b)
breadboards: 1

parts:
  Z-uno_2_1 = zuno2
  Часть1 = BH1750

nets:
  N1: Z-uno_2_1.connector2, Часть1.connector8
  N2: Z-uno_2_1.connector3, Часть1.connector9
  N3: Z-uno_2_1.connector15, Z-uno_2_1.connector16
  N4: Z-uno_2_1.connector17, Z-uno_2_1.connector18, Часть1.connector10
  N5: Z-uno_2_1.connector19, Часть1.connector12
  N6: Z-uno_2_1.connector41, Z-uno_2_1.connector44
  N7: Z-uno_2_1.connector42, Z-uno_2_1.connector43
