# Fritzing sketch id4585_Z_Uno_IR_Sharp_0 (saved by Fritzing 0.9.2b)
breadboards: 1

parts:
  Z-uno_2_1 = zuno2
  J1 = Infrared Proximity Sensor

nets:
  N1: Z-uno_2_1.connector2, J1.Vcc
  N2: Z-uno_2_1.connector3, J1.GND
  N3: Z-uno_2_1.connector10, J1.Vout
  N4: Z-uno_2_1.connector17, Z-uno_2_1.connector18
  N5: Z-uno_2_1.connector41, Z-uno_2_1.connector44
  N6: Z-uno_2_1.connector42, Z-uno_2_1.connector43
