# Fritzing sketch id4586_IR2ZWave_Z_Uno_0 (saved by Fritzing 0.9.2b)
breadboards: 1

parts:
  Z-uno_2_1 = zuno2
  IR1 = TSOP312.., 314.. [package=THT]

nets:
  N1: Z-uno_2_1.connector3, IR1.GND
  N2: Z-uno_2_1.connector4, IR1.Vs
  N3: Z-uno_2_1.connector14, IR1.Data
  N4: Z-uno_2_1.connector17, Z-uno_2_1.connector18
  N5: Z-uno_2_1.connector41, Z-uno_2_1.connector44
  N6: Z-uno_2_1.connector42, Z-uno_2_1.connector43
