# Fritzing sketch id4587_Z_Wave_Z_Uno_multiple_ds18b20_0 (saved by Fritzing 0.9.2b)
breadboards: 1

parts:
  Z-uno_2_1 = zuno2
  DS1 = DS18B20 1-Wire Temperature Sensor [part_number=DS18B20]
  DS2 = DS18B20 1-Wire Temperature Sensor [part_number=DS18B20]
  DS3 = DS18B20 1-Wire Temperature Sensor [part_number=DS18B20]
  R2 = Resistor [tolerance=±5% resistance=4.7k package=THT]

nets:
  GND: Z-uno_2_1.connector2, DS1.GND, DS2.GND, DS3.GND, R2.Pin_1
  VDD: Z-uno_2_1.connector3, DS1.VDD, DS2.VDD, DS3.VDD
  N1: Z-uno_2_1.connector15, Z-uno_2_1.connector16
  N2: Z-uno_2_1.connector17, Z-uno_2_1.connector18
  N3: Z-uno_2_1.connector20, DS1.DQ, DS2.DQ, DS3.DQ, R2.Pin_0
  N4: Z-uno_2_1.connector41, Z-uno_2_1.connector44
  N5: Z-uno_2_1.connector42, Z-uno_2_1.connector43
