# Fritzing sketch id4589_Z_Wave_Z_Uno_keypad_0 (saved by Fritzing 0.9.2b)
breadboards: 1

parts:
  Z-uno_2_1 = zuno2
  Keypad4x1 = Keypad4x4

nets:
  N1: Z-uno_2_1.connector15, Z-uno_2_1.connector16
  N2: Z-uno_2_1.connector17, Z-uno_2_1.connector18, Keypad4x1.connector8
  N3: Z-uno_2_1.connector19, Keypad4x1.connector7
  N4: Z-uno_2_1.connector20, Keypad4x1.connector6
  N5: Z-uno_2_1.connector21, Keypad4x1.connector5
  N6: Z-uno_2_1.connector36, Keypad4x1.connector4
  N7: Z-uno_2_1.connector37, Keypad4x1.connector2
  N8: Z-uno_2_1.connector38, Keypad4x1.connector1
  N9: Z-uno_2_1.connector39, Keypad4x1.connector0
  N10: Z-uno_2_1.connector41, Z-uno_2_1.connector44
  N11: Z-uno_2_1.connector42, Z-uno_2_1.connector43
