# Fritzing sketch id458_Dual_Axis_Turret._0 (saved by Fritzing 0.9.3b)
breadboards: 1

parts:
  Part1 = Arduino Mega 2560 (Rev3)
  VCC1 = 4 x AAA Battery Mount
  Part2 = Thumb Joystick
  J1 = Basic Servo
  J2 = Basic Servo
  S1 = Pushbutton [package="[SMD]"]
  LED1 = smd LED [color="Red (633nm)" package="0805 [SMD]"]
  R1 = Resistor [tolerance=±5% resistance=220 package=THT]

nets:
  N1: Part1.D10_PWM, R1.Pin_1
  5V: Part1.5V, Part2.VCC
  N2: Part1.D3_PWM, S1.Pin_3, S1.Pin_4
  N3: Part1.D5_PWM, J1.pulse
  N4: Part1.D7_PWM, J2.pulse
  VCC: VCC1.-, J1.vcc, J2.vcc
  GND: VCC1.+, J1.gnd, J2.gnd
  N5: Part2.GND, S1.Pin_1, S1.Pin_2, LED1.cathode
  N6: LED1.anode, R1.Pin_0
