# Fritzing sketch id4590_ZWave2IR_Z_Uno_0 (saved by Fritzing 0.9.2b)
breadboards: 1

parts:
  Z-uno_2_1 = zuno2
  LED4 = smd LED [color="Infrared (940nm)" package="0603 [SMD]"]  # not connected
  R1 = Resistor [tolerance=±5% resistance=330 package="2010 [SMD]"]

nets:
  N1: Z-uno_2_1.connector13, R1.Pin_0
  N2: Z-uno_2_1.connector15, Z-uno_2_1.connector16
  N3: Z-uno_2_1.connector17, Z-uno_2_1.connector18
  N4: Z-uno_2_1.connector41, Z-uno_2_1.connector44
  N5: Z-uno_2_1.connector42, Z-uno_2_1.connector43
