# Fritzing sketch id4591_Zalgo_0 (saved by Fritzing 0.7.4b)
breadboards: 1

parts:
  VCC1 = Battery
  VCC2 = Battery  # not connected
  VCC3 = Battery  # not connected
  VCC4 = Battery
  VCC5 = Battery  # not connected
  VCC6 = Battery  # not connected
  VCC7 = Battery  # not connected
  VCC8 = Battery  # not connected
  Lepai_Tripath_Class-T_Hi-Fi_Audio_Mini_Amplifier_with_Power_Supply1 = _Lepai_Tripath_Class_T_Hi_Fi_Audio_Mini_Amplifier_with_Power_Supply

nets:
  N1: VCC1.+, Lepai_Tripath_Class-T_Hi-Fi_Audio_Mini_Amplifier_with_Power_Supply1.connector1
  N2: VCC4.-, Lepai_Tripath_Class-T_Hi-Fi_Audio_Mini_Amplifier_with_Power_Supply1.connector0
