# Fritzing sketch id4592_zapper_0 (saved by Fritzing 0.9.3b)
breadboards: 1

parts:
  U1 = mystery part, 3 pins [chip_label=?]
  R1 = Rotary Potentiometer (Small) [maximum_resistance=100kΩ package=THT]
  VCC1 = Battery
  R2 = Resistor [tolerance=±5% resistance=220 package=THT]
  S1 = Pushbutton [package=THT]
  LED1 = LED - 5mm [color="Red (633nm)" package="5 mm [THT]"]
  R3 = Resistor [tolerance=±5% resistance=220 package=THT]

nets:
  N1: U1.pin1, S1.leg1, R3.Pin_1
  N2: U1.pin2, R1.leg2
  N3: U1.pin3, R2.Pin_1
  N4: R1.leg1, R2.Pin_0
  N5: VCC1.-, LED1.cathode
  N6: VCC1.+, S1.leg0
  N7: LED1.anode, R3.Pin_0
