# Fritzing sketch id4593_bombe_0 (saved by Fritzing 0.8.3b)
breadboards: 1

parts:
  Q1 = Basic FET P-Channel [package="TO220 [THT]"]  # not connected
  Q2 = PNP-Transistor [package="TO92 [THT]"]  # not connected
  IC1 = PICAXE-08 [package=THT]  # not connected
  Bauteil1 = DeuLigne 1.1 - The Snootlab's LCD shield for Arduino
  LED1 = LED - 5mm [color="Red (633nm)" package="5 mm [THT]"]
  J1 = Piezo Speaker
  M1 = Stepper Motor - Bipolar  # not connected
  Power_RGB1 = Prolight RGB 3 Watt Star  # not connected
  Bauteil2 = Arduino Pro  # not connected
  Propeller1 = Parallax Propeller D40 [package="DIP [THT]"]  # not connected

nets:
  N1: Bauteil1.A0, LED1.cathode
  N2: Bauteil1.A1, LED1.anode
  N3: Bauteil1.+5V, J1.pin1
  N4: Bauteil1.GND, J1.pin2
