# Fritzing sketch id4595_zb_0 (saved by Fritzing 0.9.3b)

parts:
  Raspberry_Pi_Zero1 = Raspberry Pi Zero
  U1 = BATTERY-2 [package=battery-aa]  # not connected
  U2 = BATTERY-2 [package=battery-aa]  # not connected
  U3 = TCM8240MD [package=tcm8240md]  # not connected
  M1 = DC Motor
  M2 = DC Motor
  S1 = SPST Switch [package=switche-dpdt]  # not connected
  LED1 = LED - 5mm [color="Red (633nm)" package="5 mm [THT]"]  # not connected
  LED2 = LED - 5mm [color="Red (633nm)" package="5 mm [THT]"]  # not connected
  R1 = Resistor [tolerance=±5% resistance=220 package="1206 [SMD]"]  # not connected
  R2 = Resistor [tolerance=±5% resistance=220 package="1206 [SMD]"]  # not connected
  Part1 = adafruit [part_number="Adafruit #1083"]
  Part2 = Monster Moto Shield

nets:
  N1: Raspberry_Pi_Zero1.3v3, Part1.connector19
  N2: Raspberry_Pi_Zero1.GPIO2, Part1.connector16
  N3: Raspberry_Pi_Zero1.GPIO3, Part1.connector17
  N4: Raspberry_Pi_Zero1.GPIO4, Part2.CS2_-_A3
  N5: Raspberry_Pi_Zero1.GPIO17, Part2.CS1_-_A2
  N6: Raspberry_Pi_Zero1.GPIO27, Part2.EN2_-_A1
  N7: Raspberry_Pi_Zero1.GPIO18, Part2.A4
  N8: M1.pin_1, Part2.OUTA2
  N9: M1.pin_2, Part2.OUTB2
  N10: M2.pin_1, Part2.OUTA1
  N11: M2.pin_2, Part2.OUTB1
