# Fritzing sketch id4596_KnockKnock_0 (saved by Fritzing 0.9.3b)
breadboards: 2

parts:
  Piezo = Piezo Speaker
  R2 = Resistor [tolerance=±5% resistance=1M package=THT]
  LED2 = LED - 5mm [color="Red (633nm)" package="5 mm [THT]"]
  R3 = Resistor [tolerance=±5% resistance=220 package=THT]
  Part5 = PlayfulTechnology_KY-038
  Part6 = KY-006
  Part7 = Arduino Uno (Rev3)
  LED3 = LED - 5mm [color="Red (633nm)" package="5 mm [THT]"]
  R5 = Resistor [tolerance=±5% resistance=220 package=THT]
  Buzzer = KY-006
  R6 = Resistor [tolerance=±5% resistance=165 package=THT]
  R7 = Resistor [tolerance=±5% resistance=165 package=THT]
  Part4 = Arduino Uno (Rev3)
  D1 = Zener Diode [part_number=1N4733 breakdown_voltage=5.1V package="300 mil [THT]"]
  Relay = keyes
  Relay1 = keyes
  L1 = PlayfulTechnology_Maglock
  L2 = PlayfulTechnology_Maglock
  JACK1 = 2.1mm_Barrel_Jack_with_Terminal_Block
  JACK2 = 2.1mm_Barrel_Jack_with_Terminal_Block

nets (from the schematic view):
  N1: Piezo.pin1, R2.Pin_1, Part7.GND, LED3.cathode, Buzzer.connector2, D1.anode, Relay1.connector2
  N2: Piezo.pin2, R2.Pin_0, Part7.A0, D1.cathode
  N3: LED2.cathode, Part5.connector1, Part6.connector2, Part4.GND, Relay.connector2
  N4: LED2.anode, R3.Pin_0
  N5: R3.Pin_1, Part4.D13/SCK
  N6: Part5.connector0, Part4.A0
  N7: Part5.connector2, Part4.5V, Relay.connector1
  N8: Part6.connector0, R6.Pin_0
  N9: Part7.D12/MISO, R7.Pin_1
  N10: Part7.D13/SCK, R5.Pin_1
  N11: Part7.D4, Relay1.connector0
  N12: Part7.5V, Relay1.connector1
  N13: LED3.anode, R5.Pin_0
  N14: Buzzer.connector0, R7.Pin_0
  N15: R6.Pin_1, Part4.D12/MISO
  N16: Part4.D4, Relay.connector0
  N17: Relay.connector3, JACK1.connector1
  N18: Relay.connector4, L2.connector1
  N19: Relay1.connector3, JACK2.connector1
  N20: Relay1.connector4, L1.connector1
  N21: L1.connector0, JACK2.connector2
  N22: L2.connector0, JACK1.connector2

notes:
  Piezo buzzers are made of crystals which flex when an electric current is applied (from "piezein" - Greek for "squeeze"). So they can be used as an ouput by supplying them with an oscillating voltage to make a sound.
  The reverse is also true - if piezoelectric crystals are vibrated, they generate a voltage, and that's how a piezo can be used as a knock detector. There are two additional components we'll also use:
  - The 1MΩ resistor is connected from the +ve lead of the piezo to GND, and is used to provide a path to discharge the voltage from the piezo (in the same way as you discharge a capacitor).
  - The 1N4733 Zener diode protects the Arduino pin from overvoltage. The voltage generated by a loud knock on the piezo can be surprisingly large - up to 90V! The Zener diode is placed with its anode connected to ground and its cathode to the +ve of the piezo. This has no effect in the circuit until a threshold is reached (5.1V, in this case), at which point it creates a short circuit to ground, allowing current from any high voltage surge to flow directly to ground rather than into the Arduino.
