# Fritzing sketch id4597_bangle_0 (saved by Fritzing 0.9.0b)
breadboards: 1

parts:
  U1 = Vibration Motor- ROB-08449 [part_number="Vibe 1201" package=vibe-motor-10mm]
  FLORA1 = Adafruit_Flora
  U2 = Vibration Motor- ROB-08449 [package=vibe-motor-10mm]
  U3 = Vibration Motor- ROB-08449 [package=vibe-motor-10mm]
  U4 = LIPO-1000mAh [package=lipo-1000]
  U5 = TRANSISTOR_NPN_2 [part_number=2N2222 package=to-92]
  U6 = TRANSISTOR_NPN_2 [part_number=2N2222 package=to-92]
  U7 = TRANSISTOR_NPN_2 [part_number=2N2222 package=to-92]
  S1 = Tilt Switch [part_number=tilt package=THT]

nets (from the schematic view):
  N1: U1.+, FLORA1.connector8, U2.+, U3.+, U4.+
  N2: U1.-, U7.C
  N3: FLORA1.connector1, U4.-, U5.E, U6.E, U7.E
  N4: FLORA1.connector9, S1.Pin_1
  N5: FLORA1.connector10, U5.B
  N6: FLORA1.connector11, S1.Pin_2
  N7: FLORA1.connector12, U6.B
  N8: FLORA1.connector13, U7.B
  N9: U2.-, U5.C
  N10: U3.-, U6.C

notes:
  LiPO is approximate
  Analog (PWM) pins:
  D3(SCL)
  A10(D10)
  A9(D9)
  A7(D6)
  A11(D12)
