# Fritzing sketch id459_violin_v2_0 (saved by Fritzing 0.9.3b)
circuit board: 8.46667cm x 5.64444cm
perfboards: 1

parts:
  Часть1 = Arduino Due (Rev2b)
  M2 = Stepper Motor - Bipolar  # not connected
  M3 = Stepper Motor - Bipolar
  M4 = Stepper Motor - Bipolar  # not connected
  J1 = Basic Servo
  J2 = Basic Servo
  J9 = double row female pin header, 6 pins [form="♀ (female)"]  # not connected
  J11 = double row female pin header, 8 pins [form="♀ (female)"]  # not connected
  J12 = double row female pin header, 8 pins [form="♀ (female)"]  # not connected
  U1 = L298 [package=multiwatt15_6400bgheatsink]
  5V = 4 x AAA Battery Mount
  12V = 4 x AAA Battery Mount
  J10 = double row female pin header, 8 pins [form="♀ (female)"]  # not connected

nets:
  N1: Часть1.D2_PWM, J2.pulse
  N2: Часть1.D3_PWM, J1.pulse
  N3: Часть1.D24, U1.IN4
  N4: Часть1.D26, U1.IN3
  N5: Часть1.D28, U1.IN2
  N6: Часть1.D30, U1.IN1
  N7: M3.A, U1.OUT1
  N8: M3.C, U1.OUT2
  N9: M3.B, U1.OUT3
  N10: M3.D, U1.OUT4
  GND: J1.gnd, J2.gnd
  VCC: J1.vcc, J2.vcc
  N11: U1.VS, 12V.+
  N12: U1.ENA, U1.VLS, U1.ENB, 5V.+
