# Fritzing sketch id45_RPi_LCD_Verbindung_V3___final_1_0 (saved by Fritzing 0.9.2b)
stripboards: 1

parts:
  U1 = LCD-16X2 [package=lcd-16x2_noholes]
  S1 = Pushbutton [package="[THT]"]
  LED1 = LED - 5mm [color="Red (633nm)" package="5 mm [THT]"]
  R4 = Trimmer Potentiometer [maximum_resistance=10kΩ package=THT]
  R5 = Resistor [tolerance=±5% resistance=220 package="0805 [SMD]"]
  C1 = Ceramic Capacitor [capacitance=100nF package="100 mil [THT, multilayer]"]
  Raspberry_Pi1 = Raspberry Pi 2
  R3 = Trimmer Potentiometer [maximum_resistance=10kΩ package=THT]
  U2 = Voltage Regulator - 5V [package="TO220 [THT]"]
  S2 = Pushbutton [package=THT]
  J1 = Screw terminal - 2 pins [package=THT]

nets:
  GND: U1.VSS, LED1.cathode, R4.leg1, C1.1, Raspberry_Pi1.GND, R3.leg1, U2.GND, J1.pin1
  N1: U1.VO, R4.wiper
  N2: U1.DB5, Raspberry_Pi1.GPIO6
  N3: U1.DB6, Raspberry_Pi1.GPIO17
  N4: U1.DB7, Raspberry_Pi1.GPIO18
  N5: S1.Pin_1, S1.Pin_2, U2.output_voltage
  N6: S1.Pin_3, S1.Pin_4, R5.Pin_1, Raspberry_Pi1.GPIO26
  N7: LED1.anode, R5.Pin_0
  N8: R4.leg2, C1.0, R3.leg2, U2.input_voltage, S2.leg0
  N9: Raspberry_Pi1.5V, S2.leg1, J1.pin2

notes:
  5V
  GND
  3,3V
  backlit
  contrast
  RS   E   D4  D5  D6  D7
  220 Ohm
  LED
  GPIO 12  21  5     6   17  18
