# Fritzing sketch id4600_Coordinator_API_0 (saved by Fritzing 0.8.3b)

parts:
  Raspberry_Pi_rev1 = Raspberry Pi rev2
  U1 = XBEE-1 [package=xbee-1]

nets:
  3V3: Raspberry_Pi_rev1.3V3, U1.VDD
  GND: Raspberry_Pi_rev1.GND, U1.GND
  N1: Raspberry_Pi_rev1.GPIO_14, U1.DIN
  N2: Raspberry_Pi_rev1.GPIO_15, U1.DOUT

notes:
  MODEL = XB24-ZB
  function set = ZIGBEE COORDINATOR API
  version = 21A7
  ID = 1234
  DH = 0
  DL = 0
  D0 = 0 (disabled)
  D1 =0 (disabled)
  IR = not set
  IC = 0 (not set)
