# Fritzing sketch id4601_Router_AT_0 (saved by Fritzing 0.8.3b)
breadboards: 1

parts:
  U1 = XBee
  VCC1 = Battery
  R1 = Resistor 50 OHM
  R2 = Resistor 50 OHM
  S1 = Pushbutton [package="[THT]"]
  S3 = Pushbutton [package="[THT]"]

nets:
  N1: U1.VCC, VCC1.+, S1.Pin_1, S1.Pin_2, S3.Pin_3, S3.Pin_4
  N2: U1.GND, VCC1.-, R1.connector0, R2.connector1
  N3: U1.pin20, R1.connector1, S1.Pin_3, S1.Pin_4
  N4: R2.connector0, S3.Pin_1, S3.Pin_2

notes:
  MODEL = XB24-ZB
  function set = ZIGBEE ROUTER AT
  version = 22A7
  ID = 1234
  DH = 13A200 (my Coordinator High adress)
  DL = 40A8C302 (my Coordinator Low adress)
  D0 = 3 (digital input)
  D1 =3 (digital input)
  IR = 500
  IC = FFFF
  2 x 1,5 Volt = 3 VCC
  R1 = 2200 OHM
  R2 = 2200 OHM
