# Fritzing sketch id4605_zx81_Raspberry_0 (saved by Fritzing 0.9.2b)
circuit board: 9.44631cm x 6.86369cm

parts:
  C1 = Ceramic Capacitor [capacitance=0.1µF package="100 mil [THT, multilayer]"]
  IC2 = IC, DIP package, 20 pins [chip_label=74HC245]
  IC1 = IC, DIP package, 20 pins [chip_label=74HC245]
  KBD = shrouded pin header, 14 pins [form="♂ (shrouded male)"]
  R1 = Resistor [tolerance=±5% resistance=10k package=THT]
  R2 = Resistor [tolerance=±5% resistance=10k package=THT]
  D8 = Rectifier Diode [part_number=1N4448 package="300 mil [THT]"]
  D9 = Rectifier Diode [part_number=1N4448 package="300 mil [THT]"]
  D10 = Rectifier Diode [part_number=1N4448 package="300 mil [THT]"]
  D11 = Rectifier Diode [part_number=1N4448 package="300 mil [THT]"]
  ZX81T = male pin header, 23 pins [form="♂ (male)"]
  ZX81B = male pin header, 23 pins [form="♂ (male)"]
  D12 = Rectifier Diode [part_number=1N4448 package="300 mil [THT]"]
  D13 = Rectifier Diode [part_number=1N4448 package="300 mil [THT]"]
  D14 = Rectifier Diode [part_number=1N4448 package="300 mil [THT]"]
  D15 = Rectifier Diode [part_number=1N4448 package="300 mil [THT]"]
  D16 = Rectifier Diode [part_number=1N4448 package="300 mil [THT]"]
  JOY = shrouded pin header, 10 pins [form="♂ (shrouded male)"]
  D17 = Rectifier Diode [part_number=1N4448 package="300 mil [THT]"]
  D18 = Rectifier Diode [part_number=1N4448 package="300 mil [THT]"]
  D19 = Rectifier Diode [part_number=1N4448 package="300 mil [THT]"]
  D20 = Rectifier Diode [part_number=1N4448 package="300 mil [THT]"]
  D21 = Rectifier Diode [part_number=1N4448 package="300 mil [THT]"]

nets:
  GND: C1.0, IC2.pin1, IC2.pin10, IC1.pin1, IC1.pin10, ZX81B.pin4, ZX81B.pin5
  N1: C1.1, IC1.pin20, ZX81B.pin1
  N2: IC2.pin2, ZX81T.pin4
  N3: IC2.pin3, ZX81T.pin5
  N4: IC2.pin4, ZX81T.pin6
  N5: IC2.pin5, ZX81T.pin9
  N6: IC2.pin6, ZX81T.pin10
  N7: IC2.pin7, ZX81T.pin1
  N8: IC2.pin8, D15.cathode
  N9: IC2.pin9, D16.cathode
  N10: IC2.pin11, ZX81B.pin16
  N11: IC2.pin12, ZX81B.pin15
  N12: IC2.pin19, R1.Pin_1, D8.cathode
  5V: IC2.pin20, R2.Pin_1
  N13: IC1.pin2, D14.cathode
  N14: IC1.pin3, D13.cathode
  N15: IC1.pin4, D12.cathode
  N16: IC1.pin5, D11.cathode
  N17: IC1.pin6, D10.cathode
  JOY8: IC1.pin7, D9.cathode
  N18: IC1.pin8, D8.anode
  N19: IC1.pin9, R1.Pin_0, R2.Pin_0
  N20: IC1.pin11, ZX81B.pin7
  N21: IC1.pin12, ZX81T.pin16
  N22: IC1.pin13, ZX81B.pin17
  N23: IC1.pin14, ZX81B.pin18
  N24: IC1.pin15, ZX81B.pin11
  N25: IC1.pin16, ZX81B.pin12
  N26: IC1.pin17, ZX81B.pin13
  N27: IC1.pin18, ZX81B.pin14
  N28: IC1.pin19, ZX81T.pin15
  N29: KBD.pin1, D10.anode
  N30: KBD.pin2, D9.anode
  N31: KBD.pin3, D16.anode
  N32: KBD.pin4, D15.anode
  N33: KBD.pin5, D14.anode
  N34: KBD.pin6, D13.anode
  N35: KBD.pin7, D12.anode
  N36: KBD.pin8, D11.anode
  N37: KBD.pin9, D17.anode
  N38: KBD.pin10, D18.anode
  N39: KBD.pin11, D19.anode
  N40: KBD.pin12, D20.anode
  N41: KBD.pin13, D21.anode
  N42: JOY.pin1, D18.cathode
  N43: JOY.pin2, D19.cathode
  N44: JOY.pin3, D20.cathode
  N45: JOY.pin4, D21.cathode
  N46: JOY.pin8, D17.cathode

notes:
  -------
