# Fritzing sketch id4606_zynthian_2in1_0 (saved by Fritzing 0.8.7b)
circuit board: 5.24017cm x 1.76117cm
breadboards: 1

parts:
  R1 = Resistor [tolerance=±5% resistance=1k package=THT]
  R2 = Resistor [tolerance=±5% resistance=10k package=THT]
  D1 = Rectifier Diode [part_number=1N4148 package="300 mil [THT]"]
  R3 = Resistor [tolerance=±5% resistance=220 package=THT]
  MIDI-IN = Header 2 [package=molex-1x2_lock]
  C1 = Ceramic Capacitor [capacitance=100nF package="100 mil [THT, multilayer]"]
  C2 = Ceramic Capacitor [capacitance=100nF package="100 mil [THT, multilayer]"]
  6N138 = zynthian
  MCP23008 = 986983750fb6cc3e2e4c0ab419dde591 [part_number=MCP23008]
  GPIO-ext = male pin header, 8 pins [form="♂ (male)"]
  RBPi = male pin header, 6 pins [form="♂ (male)"]

nets:
  N1: R1.Pin_0, 6N138.connector5, RBPi.pin2
  N2: R1.Pin_1, C2.1, 6N138.connector7
  N3: R2.Pin_0, 6N138.connector6
  N4: R2.Pin_1, C1.1, C2.0, 6N138.connector4, MCP23008.connector3, MCP23008.connector4, MCP23008.connector5, MCP23008.connector9, RBPi.pin6
  N5: D1.cathode, R3.Pin_1, 6N138.connector1
  N6: D1.anode, MIDI-IN.2, 6N138.connector2
  N7: R3.Pin_0, MIDI-IN.1
  N8: C1.0, MCP23008.connector6, MCP23008.connector18, RBPi.pin5
  N9: MCP23008.connector1, RBPi.pin4
  N10: MCP23008.connector2, RBPi.pin3
  N11: MCP23008.connector10, GPIO-ext.pin8
  N12: MCP23008.connector11, GPIO-ext.pin7
  N13: MCP23008.connector12, GPIO-ext.pin6
  N14: MCP23008.connector13, GPIO-ext.pin5
  N15: MCP23008.connector14, GPIO-ext.pin4
  N16: MCP23008.connector15, GPIO-ext.pin3
  N17: MCP23008.connector16, GPIO-ext.pin2
  N18: MCP23008.connector17, GPIO-ext.pin1
