# Fritzing sketch id4607_zynthian_controller_0 (saved by Fritzing 0.8.7b)
circuit board: 1.8cm x 6.25cm
breadboards: 1

parts:
  ENC1 = Rotary_Encoder_with_Knob
  ENC2 = Rotary_Encoder_with_Knob
  RBPi = Header 6 [package=molex-1x6_lock]
  C1 = Ceramic Capacitor [capacitance=100nF package="100 mil [THT, multilayer]"]
  C2 = Ceramic Capacitor [capacitance=100nF package="100 mil [THT, multilayer]"]
  SW2 = Header 2 [package=molex-1x2_lock]

nets:
  N1: ENC1.connector1, RBPi.1
  GND: ENC1.connector2, ENC1.connector5, ENC2.connector2, ENC2.connector5, RBPi.6, C1.0, C2.1, SW2.1
  N2: ENC1.connector3, RBPi.2
  N3: ENC1.connector4, RBPi.3, C1.1
  N4: ENC2.connector1, RBPi.4
  N5: ENC2.connector3, RBPi.5
  N6: ENC2.connector4, C2.0, SW2.2
