# Fritzing sketch id460_ArduinoAsISP_0 (saved by Fritzing 0.8.7b)
breadboards: 1

parts:
  パーツ1 = Arduino Uno (Rev3)
  U1 = atmega328 [package=dip]
  R1 = Resistor [tolerance=±5% resistance=220 package=THT]
  LED1 = LED - 5mm [color="Red (633nm)" package="5 mm [THT]"]

nets:
  N1: パーツ1.D10_PWM/SS, U1.RESET
  N2: パーツ1.D11_PWM/MOSI, U1.D11_(PWM)
  N3: パーツ1.D12/MISO, U1.D12
  N4: パーツ1.D13/SCK, U1.D13
  N5: パーツ1.RESET, R1.Pin_0
  5V: パーツ1.5V, U1.VCC, U1.AVCC, R1.Pin_1
  GND: パーツ1.GND, U1.GND, LED1.cathode
  N6: U1.D0_(RX), LED1.anode
