# Fritzing sketch id461_Arduino_1Sheeld_progetto_vibrazione_con_sensore_pir_0 (saved by Fritzing 0.9.2b)

parts:
  1Sheeld1 = 1Sheeld
  PIR1 = pir
  Componente1 = Arduino Uno (Rev3)

nets:
  N1: 1Sheeld1.connector0, Componente1.D0/RX
  N2: 1Sheeld1.connector1, Componente1.D1/TX
  N3: 1Sheeld1.connector2, PIR1.connector2, Componente1.D2
  N4: 1Sheeld1.connector3, Componente1.D3_PWM
  N5: 1Sheeld1.connector4, Componente1.D4
  N6: 1Sheeld1.connector5, Componente1.D5_PWM
  N7: 1Sheeld1.connector6, Componente1.D6_PWM
  N8: 1Sheeld1.connector7, Componente1.D7
  N9: 1Sheeld1.connector9, Componente1.D8
  N10: 1Sheeld1.connector10, Componente1.D9_PWM
  N11: 1Sheeld1.connector11, Componente1.D10_PWM/SS
  N12: 1Sheeld1.connector12, Componente1.D11_PWM/MOSI
  N13: 1Sheeld1.connector13, Componente1.D12/MISO
  N14: 1Sheeld1.connector14, Componente1.D13/SCK
  N15: 1Sheeld1.connector15, 1Sheeld1.connector26, 1Sheeld1.connector27, PIR1.connector3, Componente1.GND
  N16: 1Sheeld1.connector16, Componente1.AREF
  N17: 1Sheeld1.connector17, 1Sheeld1.connector23, Componente1.A4/SDA
  N18: 1Sheeld1.connector18, 1Sheeld1.connector24, Componente1.A5/SCL
  N19: 1Sheeld1.connector19, Componente1.A0
  N20: 1Sheeld1.connector20, Componente1.A1
  N21: 1Sheeld1.connector21, Componente1.A2
  N22: 1Sheeld1.connector22, Componente1.A3
  N23: 1Sheeld1.connector25, Componente1.VIN
  N24: 1Sheeld1.connector28, PIR1.connector1, Componente1.5V
  N25: 1Sheeld1.connector29, Componente1.3V3
  N26: 1Sheeld1.connector30, Componente1.RESET
  N27: 1Sheeld1.connector31, Componente1.ioref
  N28: 1Sheeld1.connector32, Componente1.N/C
