# Fritzing sketch id462_LCD_Thermometer_0 (saved by Fritzing 0.9.3b)
breadboards: 1

parts:
  LCD1 = LCD screen [part_number=333]  # not connected
  R1 = Rotary Potentiometer (Small) [maximum_resistance=100kΩ package=THT]
  T1 = LM35 Temperature Sensor [package="TO92 [THT]"]
  Part1 = Arduino Uno (Rev3)

nets:
  N1: R1.leg1, T1.+Vs
  N2: R1.leg2, T1.GND
  N3: T1.Vout, Part1.A0
