# Fritzing sketch id464_Arduino_ESP_8266_0 (saved by Fritzing 0.9.3b)
breadboards: 1

parts:
  Part1 = Arduino Uno (Rev3)
  U1 = ESP8266 WiFi Module [part_number=ESP8266]
  R1 = Resistor [tolerance=±5% resistance=220 package="0603 [SMD]"]

nets:
  N1: Part1.D0/RX, U1.TXD
  N2: Part1.D1/TX, U1.RXD
  3V3: Part1.3V3, U1.VCC, U1.GPIO_0, U1.GPIO_2, U1.CH_PD, U1.REST, R1.Pin_0
  GND: Part1.GND, U1.GND, R1.Pin_1
