# Fritzing sketch id465_Arduino_Mega___Module_interface_V2_0 (saved by Fritzing 0.8.3b)
circuit board: 5.35689cm x 5.1035cm
breadboards: 1

parts:
  MAX3082 = IC, DIP package, 8 pins [chip_label=IC]
  2xUltrasonic_or_8_ports = shrouded pin header, 12 pins [form="♂ (shrouded male)"]
  Diag = LED - 5mm [color="Red (633nm)" package="5 mm [THT]"]
  Com_port = shrouded pin header, 10 pins [form="♂ (shrouded male)"]
  C1 = Ceramic Capacitor [capacitance=100nF package="100 mil [THT, multilayer]"]
  J1 = female pin header, 8 pins [form="♀ (female)"]
  J2 = female pin header, 8 pins [form="♀ (female)"]
  J3 = female pin header, 8 pins [form="♀ (female)"]
  J6 = female pin header, 8 pins [form="♀ (female)"]  # not connected
  J5 = female pin header, 18 pins [form="♀ (female)"]
  L8 = Screw terminal - 2 pins [package=THT]
  J7 = Screw terminal - 2 pins [package=THT]
  L10 = Screw terminal - 2 pins [package=THT]
  L11 = Screw terminal - 2 pins [package=THT]
  T1 = mystery part, 3 pins [chip_label=BD135 spacing=300mil part_number=BD135]
  T2 = mystery part, 3 pins [chip_label=BD135 spacing=300mil part_number=BD135]
  T3 = mystery part, 3 pins [chip_label=BD135 spacing=300mil part_number=BD135]
  T4 = mystery part, 3 pins [chip_label=BD135 spacing=300mil part_number=BD135]
  T5 = mystery part, 3 pins [chip_label=BD135 spacing=300mil part_number=BD135]
  T6 = mystery part, 3 pins [chip_label=BD135 spacing=300mil part_number=BD135]
  12xPorts_+_4xAnalog = shrouded pin header, 20 pins [form="♂ (shrouded male)"]
  Res1 = IC, DIP package, 16 pins [chip_label="Resitor Array"]
  Terminator = female pin header, 2 pins [form="♀ (female)"]
  LM7805 = Basic FET P-Channel [package="TO220 [THT]"]
  C2 = Electrolytic Capacitor [capacitance=1µF package="100 mil [THT, electrolytic]"]
  C3 = Electrolytic Capacitor [capacitance=1µF package="100 mil [THT, electrolytic]"]
  Alim_12V = Screw terminal - 2 pins [package=THT]
  J4 = female pin header, 18 pins [form="♀ (female)"]
  LM35 = LM35 Temperature Sensor [package="TO92 [THT]"]

nets:
  N1: MAX3082.pin1, J1.pin8
  N2: MAX3082.pin2, J2.pin8
  N3: MAX3082.pin3, J2.pin7
  N4: MAX3082.pin4, J1.pin7
  N5: MAX3082.pin5, 2xUltrasonic_or_8_ports.pin1, 2xUltrasonic_or_8_ports.pin3, Diag.cathode, Com_port.pin3, C1.0, J5.pin18, T1.pin3, T2.pin3, T3.pin3, T4.pin3, T5.pin3, T6.pin3, 12xPorts_+_4xAnalog.pin10, 12xPorts_+_4xAnalog.pin11, LM7805.drain, C2.-, C3.-, Alim_12V.pin1, J4.pin18, LM35.GND
  N6: MAX3082.pin6, Com_port.pin2, Com_port.pin9, Terminator.pin1
  N7: MAX3082.pin7, Com_port.pin1, Com_port.pin10, Res1.pin7
  N8: MAX3082.pin8, 2xUltrasonic_or_8_ports.pin2, 2xUltrasonic_or_8_ports.pin4, Com_port.pin4, C1.1, J5.pin1, 12xPorts_+_4xAnalog.pin1, 12xPorts_+_4xAnalog.pin20, LM7805.source, C3.+, J4.pin1, LM35.+Vs
  N9: 2xUltrasonic_or_8_ports.pin5, J4.pin17
  N10: 2xUltrasonic_or_8_ports.pin6, J4.pin16
  N11: 2xUltrasonic_or_8_ports.pin7, J4.pin15
  N12: 2xUltrasonic_or_8_ports.pin8, J4.pin14
  N13: 2xUltrasonic_or_8_ports.pin9, J4.pin13
  N14: 2xUltrasonic_or_8_ports.pin10, J4.pin12
  N15: 2xUltrasonic_or_8_ports.pin11, J4.pin11
  N16: 2xUltrasonic_or_8_ports.pin12, J4.pin10
  N17: Diag.anode, Res1.pin8
  N18: Com_port.pin5, J2.pin1
  N19: Com_port.pin6, J2.pin2
  N20: Com_port.pin7, J2.pin3
  N21: Com_port.pin8, J2.pin4
  N22: J1.pin1, Res1.pin16
  N23: J1.pin2, Res1.pin15
  N24: J1.pin3, Res1.pin14
  N25: J1.pin4, Res1.pin13
  N26: J1.pin5, Res1.pin12
  N27: J1.pin6, Res1.pin11
  N28: J2.pin5, Res1.pin9
  N29: J2.pin6, 12xPorts_+_4xAnalog.pin2
  N30: J3.pin3, LM35.Vout
  N31: J3.pin5, 12xPorts_+_4xAnalog.pin9
  N32: J3.pin6, 12xPorts_+_4xAnalog.pin8
  N33: J3.pin7, 12xPorts_+_4xAnalog.pin7
  N34: J3.pin8, 12xPorts_+_4xAnalog.pin6
  N35: J5.pin15, 12xPorts_+_4xAnalog.pin5
  N36: J5.pin16, 12xPorts_+_4xAnalog.pin4
  N37: J5.pin17, 12xPorts_+_4xAnalog.pin3
  N38: L8.pin1, L10.pin1, LM7805.gate, C2.+, Alim_12V.pin2
  N39: L8.pin2, T6.pin2
  N40: J7.pin1, T2.pin2
  N41: J7.pin2, T1.pin2
  N42: L10.pin2, T3.pin2
  N43: L11.pin1, T5.pin2
  N44: L11.pin2, T4.pin2
  N45: T1.pin1, Res1.pin1
  N46: T2.pin1, Res1.pin2
  N47: T3.pin1, Res1.pin3
  N48: T4.pin1, Res1.pin4
  N49: T5.pin1, Res1.pin5
  N50: T6.pin1, Res1.pin6
  N51: 12xPorts_+_4xAnalog.pin12, J4.pin9
  N52: 12xPorts_+_4xAnalog.pin13, J4.pin8
  N53: 12xPorts_+_4xAnalog.pin14, J4.pin7
  N54: 12xPorts_+_4xAnalog.pin15, J4.pin6
  N55: 12xPorts_+_4xAnalog.pin16, J4.pin5
  N56: 12xPorts_+_4xAnalog.pin17, J4.pin4
  N57: 12xPorts_+_4xAnalog.pin18, J4.pin3
  N58: 12xPorts_+_4xAnalog.pin19, J4.pin2
  N59: Res1.pin10, Terminator.pin2

notes:
  MDL
  29/11/13
