# Fritzing sketch id466_Flexiforce_Arduino6in_0 (saved by Fritzing 0.7.12b)
breadboards: 1

parts:
  R1 = Resistor [tolerance=±5% resistance=220 package=THT]
  Arduino1 = Arduino
  J1 = Basic Force Sensing Resistor (FSR) [package=THT]
  J2 = Basic Force Sensing Resistor (FSR) [package=THT]
  R2 = Resistor [tolerance=±5% resistance=220 package=THT]
  R3 = Resistor [tolerance=±5% resistance=220 package=THT]
  J3 = Basic Force Sensing Resistor (FSR) [package=THT]
  J4 = Basic Force Sensing Resistor (FSR) [package=THT]
  R4 = Resistor [tolerance=±5% resistance=220 package=THT]
  J5 = Basic Force Sensing Resistor (FSR) [package=THT]
  R5 = Resistor [tolerance=±5% resistance=220 package=THT]
  J6 = Basic Force Sensing Resistor (FSR) [package=THT]
  R6 = Resistor [tolerance=±5% resistance=220 package=THT]

nets:
  N1: R1.Pin_0, Arduino1.GND, R2.Pin_0, R3.Pin_0, R4.Pin_0, R5.Pin_0, R6.Pin_0
  N2: R1.Pin_1, Arduino1.A0, J1.pin_1
  N3: Arduino1.+5V, J1.pin_0, J2.pin_0, J3.pin_0, J4.pin_0, J5.pin_0, J6.pin_0
  N4: Arduino1.A1, J2.pin_1, R2.Pin_1
  N5: Arduino1.A2, R3.Pin_1, J3.pin_1
  N6: Arduino1.A3, J4.pin_1, R4.Pin_1
  N7: Arduino1.A4, J5.pin_1, R5.Pin_1
  N8: Arduino1.A5, J6.pin_1, R6.Pin_1
