# Fritzing sketch id467_Floppy_Control_0 (saved by Fritzing 0.9.1b)

parts:
  Part1 = Arduino Uno (Rev3)
  J1 = shrouded pin header, 34 pins [form="♂ (shrouded male)"]

nets:
  N1: Part1.D8, J1.pin26
  N2: Part1.D10_PWM/SS, J1.pin28
  N3: Part1.D6_PWM, J1.pin25
  N4: Part1.GND, J1.pin1
  N5: J1.pin6, J1.pin29

notes:
  On Floppy drive, all lower pins are ground
  Pin 12->13 Drive Select
  Pin 6 / 14 = Motor Enable
  Pin 8 / 18 = Direction
  Pin 10/14 = Step
