# Fritzing sketch id468_GALACTIC_FORCE_0 (saved by Fritzing 0.9.2b)
breadboards: 1

parts:
  Part1 = Arduino Uno (Rev3)
  LCD1 = LCD screen
  J1 = Piezo Speaker
  S1 = Momentary Switch [package=ksa_sealed_tac_switch]
  S2 = Momentary Switch [package=ksa_sealed_tac_switch]
  R1 = Resistor [tolerance=±5% resistance=10k package=THT]
  R2 = Resistor [tolerance=±5% resistance=10k package=THT]
  R3 = Trimmer Potentiometer [maximum_resistance=10kΩ package=THT]
  R4 = Resistor [tolerance=±5% resistance=150 package=THT]

nets:
  N1: Part1.D8, LCD1.DB7
  N2: Part1.D9_PWM, LCD1.DB6
  N3: Part1.D11_PWM/MOSI, LCD1.E
  N4: Part1.D12/MISO, LCD1.RS
  N5: Part1.D2, S1.1
  N6: Part1.D3_PWM, S2.1
  N7: Part1.D4, LCD1.DB5
  N8: Part1.D5_PWM, LCD1.DB4
  N9: Part1.D6_PWM, J1.pin2
  3V3: Part1.3V3, LCD1.VSS, LCD1.R/W, LCD1.LED-, J1.pin1, R1.Pin_0, R2.Pin_0, R3.leg2
  5V: Part1.5V, LCD1.VDD, S1.4, S2.4, R3.leg1, R4.Pin_0
  N10: LCD1.V0, R3.wiper
  N11: LCD1.LED+, R4.Pin_1
  N12: S1.2, R1.Pin_1
  N13: S2.2, R2.Pin_1
