# Fritzing sketch id469_game_read_0 (saved by Fritzing 0.7.10b)
breadboards: 1
stripboards: 1

parts:
  U1 = Arduino Mega
  R1 = Resistor [tolerance=±5% resistance=10k package=THT]
  R2 = Resistor [tolerance=±5% resistance=220 package=THT]
  R3 = Resistor [tolerance=±5% resistance=220 package=THT]
  R4 = Resistor [tolerance=±5% resistance=220 package=THT]
  R5 = Resistor [tolerance=±5% resistance=220 package=THT]
  R6 = Resistor [tolerance=±5% resistance=220 package=THT]
  R7 = Resistor [tolerance=±5% resistance=220 package=THT]
  R8 = Resistor [tolerance=±5% resistance=220 package=THT]
  R9 = Resistor [tolerance=±5% resistance=220 package=THT]
  R10 = Resistor [tolerance=±5% resistance=220 package=THT]
  R11 = Resistor [tolerance=±5% resistance=220 package=THT]
  R12 = Resistor [tolerance=±5% resistance=220 package=THT]
  R13 = Resistor [tolerance=±5% resistance=220 package=THT]
  R14 = Resistor [tolerance=±5% resistance=220 package=THT]
  R15 = Resistor [tolerance=±5% resistance=220 package=THT]
  R16 = Resistor [tolerance=±5% resistance=220 package=THT]
  R17 = Resistor [tolerance=±5% resistance=220 package=THT]
  R18 = Resistor [tolerance=±5% resistance=220 package=THT]
  R19 = Resistor [tolerance=±5% resistance=220 package=THT]
  R20 = Resistor [tolerance=±5% resistance=220 package=THT]
  R21 = Resistor [tolerance=±5% resistance=220 package=THT]
  R22 = Resistor [tolerance=±5% resistance=220 package=THT]
  R23 = Resistor [tolerance=±5% resistance=220 package=THT]
  R24 = Resistor [tolerance=±5% resistance=220 package=THT]
  R25 = Resistor [tolerance=±5% resistance=220 package=THT]
  R26 = Resistor [tolerance=±5% resistance=220 package=THT]
  R27 = Resistor [tolerance=±5% resistance=220 package=THT]
  R28 = Resistor [tolerance=±5% resistance=220 package=THT]
  R29 = Resistor [tolerance=±5% resistance=10k package=THT]
  R30 = Resistor [tolerance=±5% resistance=10k package=THT]
  R31 = Resistor [tolerance=±5% resistance=10k package=THT]
  SD_Card_Adapter1 = SD_Card_Break_out

nets:
  N1: U1.GND, R29.Pin_0, R30.Pin_0, R31.Pin_0, SD_Card_Adapter1.connector14, SD_Card_Adapter1.connector15
  N2: U1.A0, R26.Pin_1
  N3: U1.A1, R24.Pin_1
  N4: U1.A2, R23.Pin_1
  N5: U1.A3, R22.Pin_1
  N6: U1.A4, R21.Pin_1
  N7: U1.A5, R20.Pin_1
  N8: U1.D22, R9.Pin_1
  N9: U1.D23, R8.Pin_1
  N10: U1.D24, R7.Pin_1
  N11: U1.D25, R6.Pin_1
  N12: U1.D26, R5.Pin_1
  N13: U1.D27, R4.Pin_1
  N14: U1.D28, R3.Pin_1
  N15: U1.D29, R2.Pin_1
  N16: U1.D47, R25.Pin_1
  N17: U1.D48, R27.Pin_1
  N18: U1.D49, R28.Pin_1
  N19: U1.D50, SD_Card_Adapter1.connector11
  N20: U1.D51, SD_Card_Adapter1.connector10
  N21: U1.D52, SD_Card_Adapter1.connector13
  N22: U1.D53, SD_Card_Adapter1.connector9
  N23: U1.A6, R19.Pin_1
  N24: U1.A7, R18.Pin_1
  N25: U1.A8, R17.Pin_1
  N26: U1.A9, R16.Pin_1
  N27: U1.A10, R15.Pin_1
  N28: U1.A11, R14.Pin_1
  N29: U1.A12, R13.Pin_1
  N30: U1.A13, R12.Pin_1
  N31: U1.A14, R11.Pin_1
  N32: U1.A15, R10.Pin_1
  N33: U1.+5V, R1.Pin_1, SD_Card_Adapter1.connector16
  N34: R1.Pin_0, R2.Pin_0, R3.Pin_0, R4.Pin_0, R5.Pin_0, R6.Pin_0, R7.Pin_0, R8.Pin_0, R9.Pin_0, R10.Pin_0, R11.Pin_0, R12.Pin_0, R13.Pin_0, R14.Pin_0, R15.Pin_0, R16.Pin_0, R17.Pin_0, R18.Pin_0, R19.Pin_0, R20.Pin_0, R21.Pin_0, R22.Pin_0, R23.Pin_0, R24.Pin_0, R25.Pin_0, R26.Pin_0, R27.Pin_0, R28.Pin_0, R29.Pin_1, R30.Pin_1, R31.Pin_1

notes:
  Game Boy Cartridge Slot (1 - 32)
  1
  32
