# Fritzing sketch id4709_Led_Police (saved by Fritzing 0.9.3b)
breadboards: 1

parts:
  Εξάρτημα1 = Arduino Uno (Rev3)
  LED1 = LED - 5mm [color="Red (633nm)" package="5 mm [THT]"]
  LED2 = LED - 5mm [color="White (6500K)" package="5 mm [THT]"]
  LED3 = LED - 5mm [color="Blue (470nm)" package="5 mm [THT]"]
  R1 = Resistor [tolerance=±5% resistance=200 package=THT]
  R2 = Resistor [tolerance=±5% resistance=100 package=THT]
  R3 = Resistor [tolerance=±5% resistance=100 package=THT]

nets:
  N1: Εξάρτημα1.D11_PWM/MOSI, LED3.anode
  N2: Εξάρτημα1.D12/MISO, LED2.anode
  N3: Εξάρτημα1.D13/SCK, LED1.anode
  N4: Εξάρτημα1.GND, R1.Pin_0, R2.Pin_0, R3.Pin_0
  N5: LED1.cathode, R1.Pin_1
  N6: LED2.cathode, R2.Pin_1
  N7: LED3.cathode, R3.Pin_1
