# Fritzing sketch id470_arduinogopropano_0 (saved by Fritzing 0.8.7b)

parts:
  Parte1 = Arduino Uno (Rev3)
  J1 = Basic Servo

nets:
  N1: Parte1.D9_PWM, J1.pulse
  5V: Parte1.5V, J1.vcc
  GND: Parte1.GND, J1.gnd
