# Fritzing sketch id472_ON_OFF_con_Arduino_GSM_Shield_0 (saved by Fritzing 0.9.0b)
breadboards: 1

parts:
  Componente1 = Arduino Uno (Rev3)
  LED1 = LED - 5mm [color="Red (660nm)" package="5 mm [THT]"]
  R1 = Resistor [tolerance=±5% resistance=220 package=THT]
  LED2 = LED - 5mm [color="Green (570nm)" package="5 mm [THT]"]
  R2 = Resistor [tolerance=±5% resistance=220 package=THT]
  Componente2 = Arduino GSM Shield  # not connected

nets:
  N1: Componente1.D10_PWM/SS, LED1.anode
  N2: Componente1.D12/MISO, LED2.anode
  N3: Componente1.GND, R1.Pin_1, R2.Pin_1
  N4: LED1.cathode, R1.Pin_0
  N5: LED2.cathode, R2.Pin_0
