# Fritzing sketch id4735_Reading_two_IC_CNY70 (saved by Fritzing 0.9.3b)
breadboards: 1

parts:
  R1 = Resistor [tolerance=±5% resistance=220 package=THT]
  R2 = Resistor [tolerance=±5% resistance=10k package=THT]
  Componente1 = Arduino Uno (Rev3)
  IC1 = IC, DIP package, 4 pins [chip_label=IC]
  R3 = Resistor [tolerance=±5% resistance=220 package=THT]
  R4 = Resistor [tolerance=±5% resistance=10k package=THT]
  IC2 = IC, DIP package, 4 pins [chip_label=IC]

nets:
  N1: R1.Pin_0, R2.Pin_0, Componente1.GND, R3.Pin_1, R4.Pin_1
  N2: R1.Pin_1, IC1.pin1
  N3: R2.Pin_1, Componente1.A4/SDA, IC1.pin3
  N4: Componente1.A5/SCL, R4.Pin_0, IC2.pin3
  N5: Componente1.5V, IC1.pin2, IC1.pin4, IC2.pin2, IC2.pin4
  N6: R3.Pin_0, IC2.pin1
