# Fritzing sketch id4750_Amblone_ULN2003a_2 (saved by Fritzing 0.6.3b)
breadboards: 1

parts:
  ULN2003a = ULN2003A [package="DIP16 [THT]"]
  ULN2003a_2 = ULN2003A [package="DIP16 [THT]"]
  PWM = female pin header, 3 pins [form="♀ (female)"]
  PWM_2 = female pin header, 6 pins [form="♀ (female)"]
  Strip3 = female pin header, 4 pins [form="♀ (female)"]
  Strip2 = female pin header, 4 pins [form="♀ (female)"]
  Neg = female pin header, 1 pin [form="♀ (female)"]
  Strip1 = female pin header, 4 pins [form="♀ (female)"]
  Arduino_GND = female pin header, 1 pin [form="♀ (female)"]
  Pos = female pin header, 1 pin [form="♀ (female)"]

nets:
  N1: ULN2003a.In_1, PWM_2.pin1
  N2: ULN2003a.In_2, PWM_2.pin2
  N3: ULN2003a.In_3, PWM_2.pin3
  N4: ULN2003a.In_4, PWM_2.pin4
  N5: ULN2003a.In_5, PWM_2.pin5
  N6: ULN2003a.In_6, PWM_2.pin6
  N7: ULN2003a.0V, ULN2003a_2.0V, Neg.pin1, Arduino_GND.pin1
  N8: ULN2003a.Out_6, Strip2.pin3
  N9: ULN2003a.Out_5, Strip2.pin2
  N10: ULN2003a.Out_4, Strip2.pin1
  N11: ULN2003a.Out_3, Strip1.pin3
  N12: ULN2003a.Out_2, Strip1.pin2
  N13: ULN2003a.Out_1, Strip1.pin1
  N14: ULN2003a_2.In_1, PWM.pin1
  N15: ULN2003a_2.In_2, PWM.pin2
  N16: ULN2003a_2.In_3, PWM.pin3
  N17: ULN2003a_2.Out_3, Strip3.pin3
  N18: ULN2003a_2.Out_2, Strip3.pin2
  N19: ULN2003a_2.Out_1, Strip3.pin1
  N20: Strip3.pin4, Strip2.pin4, Strip1.pin4, Pos.pin1
