# Fritzing sketch id4754_Motion_Control_Project (saved by Fritzing 0.9.3b)
breadboards: 1

parts:
  hc-sr1 = hc-sr04
  hc-sr2 = hc-sr04
  Part1 = Arduino Uno (Rev3)
  Part2 = DeuLigne 1.1 - The Snootlab's LCD shield for Arduino
  S1 = Pushbutton [package="[THT]"]
  S2 = Pushbutton [package="[THT]"]
  S3 = Pushbutton [package="[THT]"]
  R1 = Resistor [tolerance=±5% resistance=10k package="0603 [SMD]"]
  R2 = Resistor [tolerance=±5% resistance=10k package="0603 [SMD]"]
  R3 = Resistor [tolerance=±5% resistance=10k package="0603 [SMD]"]

nets:
  VCC: hc-sr1.VCC, hc-sr2.VCC, Part1.A1, Part1.A3, Part1.5V, Part2.+5V, S2.Pin_1, S2.Pin_2, S3.Pin_1, S3.Pin_2, R1.Pin_0, R2.Pin_0, R3.Pin_0
  N1: hc-sr1.Trig, Part1.D11_PWM/MOSI
  N2: hc-sr1.Echo, Part1.D10_PWM/SS
  GND: hc-sr1.GND, hc-sr2.GND, Part1.GND, Part2.GND, R1.Pin_1, R2.Pin_1, R3.Pin_1
  N3: hc-sr2.Trig, Part1.D3_PWM
  N4: hc-sr2.Echo, Part1.D2
  N5: Part1.A5/SCL, S1.Pin_1, S1.Pin_2
  N6: Part1.D8, Part2.D8
  N7: Part1.D9_PWM, Part2.D9
  N8: Part1.AREF, Part2.AREF
  N9: Part1.D4, Part2.D4
  N10: Part1.D5_PWM, Part2.D5
  N11: Part1.D6_PWM, Part2.D6
  N12: Part1.D7, Part2.D7
  3V3: Part1.3V3, Part2.+3V3
  VIN: Part1.VIN, Part2.VIN
  N13: S1.Pin_3, S1.Pin_4
  N14: S2.Pin_3, S2.Pin_4
  N15: S3.Pin_3, S3.Pin_4
