# Fritzing sketch id476_Mega.IR.Power.Meter.Pulse_0 (saved by Fritzing 0.8.3b)
circuit board: 16.9333cm x 5.64444cm
breadboards: 1
stripboards: 1

parts:
  Part2 = Arduino Mega 2560 (Rev3)
  C2 = Ceramic Capacitor [capacitance=100nF package="100 mil [THT, multilayer]"]
  LED3 = LED - 3mm [color="Orange (620nm)" package="3 mm [THT]"]
  R3 = Resistor [tolerance=±5% resistance=18k package=THT]

nets:
  N1: Part2.GND, C2.0, LED3.cathode, R3.Pin_0
  N2: Part2.5V, C2.1
  N3: Part2.D24, R3.Pin_1
  N4: Part2.D26, LED3.anode
