# Fritzing sketch id477_IO_Expander_circuit_diagrams_0 (saved by Fritzing 0.9.3b)

parts:
  I2C_I/O_Expander = IC, DIP package, 28 pins [chip_label=MCP23017]
  Analog_Multiplexers_and_Demultiplexers = IC, DIP package, 16 pins [chip_label=74HC4052]
  AVR_Microcomputer = Arduino Uno (Rev3)
  R1 = Resistor [tolerance=±5% resistance=10k package=THT]
  R2 = Resistor [tolerance=±5% resistance=10k package=THT]
  Anarog_Input_device = Soil Moisture Sensor

nets:
  5V: I2C_I/O_Expander.pin9, I2C_I/O_Expander.pin18, Analog_Multiplexers_and_Demultiplexers.pin16, AVR_Microcomputer.5V, R1.Pin_0, R2.Pin_0, Anarog_Input_device.VCC
  GND: I2C_I/O_Expander.pin10, I2C_I/O_Expander.pin15, I2C_I/O_Expander.pin16, I2C_I/O_Expander.pin17, Analog_Multiplexers_and_Demultiplexers.pin6, Analog_Multiplexers_and_Demultiplexers.pin8, AVR_Microcomputer.GND, Anarog_Input_device.GND
  N1: I2C_I/O_Expander.pin12, AVR_Microcomputer.A5/SCL, R2.Pin_1
  N2: I2C_I/O_Expander.pin13, AVR_Microcomputer.A4/SDA, R1.Pin_1
  N3: I2C_I/O_Expander.pin21, Analog_Multiplexers_and_Demultiplexers.pin10
  N4: I2C_I/O_Expander.pin22, Analog_Multiplexers_and_Demultiplexers.pin9
  N5: Analog_Multiplexers_and_Demultiplexers.pin12, Anarog_Input_device.SIG
  N6: Analog_Multiplexers_and_Demultiplexers.pin13, AVR_Microcomputer.A0

notes:
  I2C I/O Expander circuit diagrams, Addition xx Digital I/O and xx Anaglog I/O., 1.0
  Pullup
  Arduino I2C I/O Expander 14 Digital I/O and 4(8) Analog input.
  #include <Wire.h> // I2C Lib.
  void setup() {
  Wire.begin(); //creates a Wire object
  Serial.begin(9600);
  // set I/O pins to outputs
  Wire.beginTransmission(0x20); //begins talking to the slave device
  Wire.write(0x00); //selects the IODIRA register
  Wire.write(0x00); //this sets all port A pins to outputs
  Wire.endTransmission(); //stops talking to device
  Wire.beginTransmission(0x20);//begins talking again to slave device
  Wire.write(0x01); //selects the IODIRB register
  Wire.write(0x00); // sets all port B pins to outputs
  Wire.endTransmission(); //ends communication with slave device
  }
  void loop()
  {
  Wire.beginTransmission(0x20); //starts talking to slave device
  Wire.write(0x12); //selects the GPIOA pins
  Wire.write(00000001); // turns on pins 0 and 1 of GPIOA
  Wire.endTransmission(); //ends communication with the device
  Wire.beginTransmission(0x20); //starts talking to slave device
  Wire.write(0x13); //selects the GPIOB pins
  Wire.write(00000001); //turns on pin 0 of GPIOA
  Wire.endTransmission();//ends communication with the device
  Serial.println(analogRead(0));
  delay(500);
  }
  n/c
  D I/O
  A In
