# Fritzing sketch id479_Bluetooth_KontrolluOda_Lambasi_0 (saved by Fritzing 0.9.2b)

parts:
  Eleman1 = Arduino Uno (Rev3)
  KY-5 = keyes
  Eleman2 = Bluetooth HC-05 Macho

nets:
  N1: Eleman1.D9_PWM, KY-5.connector2
  N2: Eleman1.D0/RX, Eleman2.TXD
  N3: Eleman1.D1/TX, Eleman2.RXD
  3V3: Eleman1.3V3, Eleman2.VCC
  N4: Eleman1.5V, KY-5.connector0
  GND: Eleman1.GND, KY-5.connector1, Eleman2.GND
