# Fritzing sketch id47_idpong_0 (saved by Fritzing 0.9.3b)
breadboards: 1

parts:
  R1 = Resistor [tolerance=±5% resistance=220 package=THT]
  R2 = Resistor [tolerance=±5% resistance=220 package=THT]
  R3 = Resistor [tolerance=±5% resistance=220 package=THT]
  R4 = Resistor [tolerance=±5% resistance=220 package=THT]
  R5 = Resistor [tolerance=±5% resistance=220 package=THT]
  R6 = Resistor [tolerance=±5% resistance=220 package=THT]
  R7 = Resistor [tolerance=±5% resistance=220 package=THT]
  R8 = Resistor [tolerance=±5% resistance=220 package=THT]
  LED1 = LED - 3mm [color="Red (633nm)" package="3 mm [THT]"]  # not connected
  LED2 = LED - 3mm [color="Red (633nm)" package="3 mm [THT]"]
  LED3 = LED - 3mm [color="Red (633nm)" package="3 mm [THT]"]
  LED4 = LED - 3mm [color="Red (633nm)" package="3 mm [THT]"]
  LED5 = LED - 3mm [color="Red (633nm)" package="3 mm [THT]"]
  LED6 = LED - 3mm [color="Red (633nm)" package="3 mm [THT]"]
  LED7 = LED - 3mm [color="Red (633nm)" package="3 mm [THT]"]
  LED8 = LED - 3mm [color="Red (633nm)" package="3 mm [THT]"]
  S1 = Pushbutton [package="[THT]"]
  S2 = Pushbutton [package="[THT]"]
  Part1 = Arduino Uno (Rev3)
  R9 = Resistor [tolerance=±5% resistance=220 package=THT]
  R10 = Resistor [tolerance=±5% resistance=220 package=THT]

nets:
  N1: R1.Pin_0, LED2.cathode
  N2: R1.Pin_1, R2.Pin_0, R3.Pin_1, R4.Pin_1, R5.Pin_0, R6.Pin_0, R7.Pin_0, R8.Pin_0, Part1.GND, R9.Pin_0, R10.Pin_1
  N3: R2.Pin_1, LED3.cathode
  N4: R3.Pin_0, LED4.cathode
  N5: R4.Pin_0, LED5.cathode
  N6: R5.Pin_1, LED6.cathode
  N7: R6.Pin_1, LED7.cathode
  N8: R8.Pin_1, LED8.cathode
  N9: LED2.anode, Part1.D6_PWM
  N10: LED3.anode, Part1.A0
  N11: LED4.anode, Part1.A1
  N12: LED5.anode, Part1.A2
  N13: LED6.anode, Part1.A3
  N14: LED7.anode, Part1.D9_PWM
  N15: LED8.anode, Part1.D5_PWM
  N16: S1.Pin_1, S1.Pin_2, S2.Pin_1, S2.Pin_2, Part1.5V
  N17: S1.Pin_3, S1.Pin_4, Part1.D10_PWM/SS, R10.Pin_0
  N18: S2.Pin_3, S2.Pin_4, Part1.D11_PWM/MOSI, R9.Pin_1
