# Fritzing sketch id4819_schemavenitolmax (saved by Fritzing 0.9.3b)
breadboards: 1

parts:
  Composant1 = Arduino Uno (Rev3)
  M1 = DC Motor
  Composant2 = IR Receiver Breakout [package=PCB]
  IC1 = L293D [package=THT]

nets:
  N1: Composant1.D2, IC1.Enable_1
  N2: Composant1.D4, IC1.In_2
  N3: Composant1.D5_PWM, IC1.In_1
  N4: Composant1.D6_PWM, Composant2.VCC
  N5: Composant1.3V3, Composant2.OUT
  N6: Composant1.5V, IC1.+Vmotor, IC1.+V
  GND: Composant1.GND, Composant2.GND, IC1.0V
  N7: M1.pin_1, IC1.Out_1_(_Controlled_by_Enable_1_)
  N8: M1.pin_2, IC1.Out_2_(_Controlled_by_Enable_1_)
