# Fritzing sketch id482_led_control_0 (saved by Fritzing 0.8.7b)
breadboards: 1

parts:
  Part2 = Arduino Ethernet Shield (Rev3)
  LED1 = LED - 5mm [color="Red (633nm)" package="5 mm [THT]"]
  LED2 = LED - 5mm [color="Yellow (585nm)" package="5 mm [THT]"]
  LED3 = LED - 5mm [color="Green (555nm)" package="5 mm [THT]"]
  LED4 = LED - 5mm [color="Green (555nm)" package="5 mm [THT]"]

nets:
  N1: Part2.GND, LED1.cathode, LED2.cathode, LED3.cathode, LED4.cathode
  N2: Part2.SDCS, LED4.anode
  N3: Part2.PWM_D5, LED3.anode
  N4: Part2.PWM_D6, LED2.anode
  N5: Part2.D7, LED1.anode
