# Fritzing sketch id483_Arduino_IR_Obstacle_Sensor_Buzzer_With_LED_0 (saved by Fritzing 0.9.3b)
breadboards: 1

parts:
  Part1 = Arduino Uno (Rev3)
  Q1 = NPN-Transistor [package="TO92 [THT]"]
  R1 = Resistor [tolerance=±5% resistance=1k package=THT]
  LED1 = LED - 5mm [color="White (4500K)" package="5 mm [THT]"]
  J1 = Piezo Speaker
  R2 = Resistor [tolerance=±5% resistance=470 package=THT]
  J2 = Infrared Proximity Sensor
  LED2 = LED - 5mm [color="Yellow (595nm)" package="5 mm [THT]"]

nets:
  N1: Part1.A5/SCL, J2.Vout, LED2.anode
  N2: Part1.D13/SCK, R1.Pin_0
  N3: Q1.E, LED1.anode
  N4: Q1.B, R1.Pin_1
  N5: Q1.C, J1.pin1
  N6: LED1.cathode, R2.Pin_1
  N7: J1.pin2, J2.Vcc
  N8: R2.Pin_0, J2.GND, LED2.cathode
