# Fritzing sketch id484_ArduinoISP_0 (saved by Fritzing 0.7.7b)
breadboards: 1

parts:
  Arduino_UNO = Arduino
  ZIF_SOCKET1 = Aries 28-6574-10 28W ZIF Socket [part_number=28-6574-10]
  LED1 = LED - 5mm [color="Orange (605nm)" package="5 mm [THT]"]
  LED3 = LED - 5mm [color="Green (555nm)" package="5 mm [THT]"]
  LED2 = LED - 5mm [color="Red (633nm)" package="5 mm [THT]"]
  R1 = Resistor [tolerance=±5% resistance=220 package=THT]
  R2 = Resistor [tolerance=±5% resistance=220 package=THT]
  R3 = Resistor [tolerance=±5% resistance=220 package=THT]

nets:
  N1: Arduino_UNO.GND, ZIF_SOCKET1.Pin_8, ZIF_SOCKET1.Pin_22, LED1.cathode, LED3.cathode, LED2.cathode
  N2: Arduino_UNO.D13, ZIF_SOCKET1.Pin_19
  N3: Arduino_UNO.D12, ZIF_SOCKET1.Pin_18
  N4: Arduino_UNO.D11, ZIF_SOCKET1.Pin_17
  N5: Arduino_UNO.D10, ZIF_SOCKET1.Pin_1
  N6: Arduino_UNO.D9, R1.Pin_1
  N7: Arduino_UNO.D8, R2.Pin_1
  N8: Arduino_UNO.D7, R3.Pin_1
  N9: Arduino_UNO.+5V, ZIF_SOCKET1.Pin_7, ZIF_SOCKET1.Pin_20
  N10: LED1.anode, R1.Pin_0
  N11: LED3.anode, R3.Pin_0
  N12: LED2.anode, R2.Pin_0
