# Fritzing sketch id485_Arduino_ISP_0 (saved by Fritzing 0.8.7b)
circuit board: 7.13328cm x 5.70832cm
breadboards: 2

parts:
  U1 = atmega168 [package=dip]
  U3 = attiny85 [package=dip]
  U2 = ATmega644 [package=pdpi]
  LED1 = LED - 5mm [color="Red (633nm)" package="5 mm [THT]"]
  LED2 = LED - 5mm [color="Red (633nm)" package="5 mm [THT]"]
  LED3 = LED - 5mm [color="Red (633nm)" package="5 mm [THT]"]
  Part1 = Arduino Uno (Rev3)
  1K = Resistor [tolerance=±5% resistance=1k package=THT]
  Y1 = Resonator [frequency="16 Mhz" package=THT]
  C1 = Ceramic Capacitor [capacitance=100nF package="100 mil [THT, multilayer]"]

nets:
  N1: U1.RESET, U3.Pin_1, U2.RESET, Part1.D10_PWM/SS, C1.1
  N2: U1.VCC, U1.AVCC, U3.Pin_8
  GND: U1.GND, U1.D13, U3.Pin_4, U3.Pin_7, U2.PB7, U2.GND, Part1.D13/SCK, Part1.GND, 1K.Pin_0, Y1.GND, C1.0
  N3: U1.XLAT1, U2.PD0, Y1.0
  N4: U1.XLAT2, U2.XTAL1, Y1.pin_1
  N5: U1.D11_(PWM), U3.Pin_5, U2.PB5, Part1.D11_PWM/MOSI
  N6: U1.D12, U3.Pin_6, U2.PB6, Part1.D12/MISO
  VCC: U2.VCC, U2.AVCC, U2.AREF, Part1.5V
  N7: LED1.cathode, LED2.cathode, LED3.cathode, 1K.Pin_1
  N8: LED1.anode, Part1.D9_PWM
  N9: LED2.anode, Part1.D8
  N10: LED3.anode, Part1.D7
