# Fritzing sketch id486_Arduino_ISP_plus_Atmega328P_0 (saved by Fritzing 0.9.2b)

parts:
  U1 = atmega328 [package=dip]
  Componente1 = Arduino Nano (Rev3.0)
  C1 = Capacitor Polarized [package=cpol-radial-10uf-25v]
  R1 = Resistor [tolerance=±5% resistance=10k package="0402 [SMD]"]  # not connected
  XTAL1 = Crystal [frequency="16 Mhz" package=THT]

nets:
  N1: U1.RESET, Componente1.D10
  VCC: U1.VCC, Componente1.5V
  GND: U1.GND, U1.A0, Componente1.GND, C1.+
  N2: U1.XLAT1, XTAL1.pin_1
  N3: U1.XLAT2, XTAL1.pin_0
  N4: U1.D11_(PWM), Componente1.D11/MOSI
  N5: U1.D12, Componente1.D12/MISO
  N6: U1.D13, Componente1.D13/SCK
  N7: Componente1.RESET, C1.-
