# Fritzing sketch id487_ISP_Shield_0 (saved by Fritzing 0.7.4b)
breadboards: 1

parts:
  Arduino1 = Arduino
  ATMEGA328 = atmega168 [package=dip]
  J1 = female pin header, 14 pins [form="♀ (female)"]
  J2 = female pin header, 14 pins [form="♀ (female)"]
  R1 = Resistor [tolerance=±5% resistance=120 package=THT]
  R2 = Resistor [tolerance=±5% resistance=10k package=THT]
  XTAL1 = Crystal [frequency="16 Mhz" package=THT]
  C1 = Ceramic Capacitor [capacitance=22nF package="100 mil [THT, multilayer]"]
  C2 = Ceramic Capacitor [capacitance=22nF package="100 mil [THT, multilayer]"]
  HB = LED - 3mm [color="Green (565nm)" package="3 mm [THT]"]
  ERR = LED - 3mm [color="Red (633nm)" package="3 mm [THT]"]
  PRG = LED - 3mm [color="Yellow (592nm)" package="3 mm [THT]"]
  R3 = Resistor [tolerance=±5% resistance=1k package=THT]
  R4 = Resistor [tolerance=±5% resistance=1k package=THT]
  R5 = Resistor [tolerance=±5% resistance=1k package=THT]
  C3 = Ceramic Capacitor [capacitance=100nF package="100 mil [THT, multilayer]"]
  J5 = female pin header, 2 pins [form="♀ (female)"]
  C4 = Ceramic Capacitor [capacitance=100nF package="100 mil [THT, multilayer]"]
  RESET = Pushbutton [package="[THT]"]
  C5 = Ceramic Capacitor [capacitance=100nF package="100 mil [THT, multilayer]"]
  FTDI = female pin header, 6 pins [form="♀ (female)"]
  C6 = Ceramic Capacitor [capacitance=100nF package="100 mil [THT, multilayer]"]
  GND = female pin header, 1 pin [form="♀ (female)"]
  RESET_2 = female pin header, 1 pin [form="♀ (female)"]
  SCK = female pin header, 1 pin [form="♀ (female)"]
  MISO = female pin header, 1 pin [form="♀ (female)"]
  MOSI = female pin header, 1 pin [form="♀ (female)"]
  Vcc = female pin header, 1 pin [form="♀ (female)"]
  PWR = LED - 3mm [color="Blue (505nm)" package="3 mm [THT]"]
  R6 = Resistor [tolerance=±5% resistance=1k package=THT]
  C4<>dir = female pin header, 3 pins [form="♀ (female)"]
  10k<>120 = female pin header, 3 pins [form="♀ (female)"]

nets:
  GND: Arduino1.GND, ATMEGA328.GND, J1.pin8, J2.pin7, C1.0, C2.1, HB.cathode, ERR.cathode, PRG.cathode, C3.1, RESET.Pin_1, RESET.Pin_2, C5.0, FTDI.pin1, GND.pin1, PWR.cathode
  N1: Arduino1.D13, ATMEGA328.D13, J2.pin10, SCK.pin1
  N2: Arduino1.D12, ATMEGA328.D12, J2.pin11, MISO.pin1
  N3: Arduino1.D11, ATMEGA328.D11_(PWM), J2.pin12, MOSI.pin1
  N4: Arduino1.D10, C4<>dir.pin2
  N5: Arduino1.D9, R5.Pin_0
  N6: Arduino1.D8, R4.Pin_0
  N7: Arduino1.D7, R3.Pin_0
  5V: Arduino1.+5V, ATMEGA328.VCC, ATMEGA328.AVCC, J1.pin7, J2.pin9, FTDI.pin3, Vcc.pin1, R6.Pin_0, 10k<>120.pin2
  N8: ATMEGA328.RESET, J1.pin1, R1.Pin_1, R2.Pin_1, J5.pin1, C4.1, RESET.Pin_3, RESET.Pin_4, C6.0, RESET_2.pin1, C4<>dir.pin1
  N9: ATMEGA328.D0_(RX), J1.pin2, FTDI.pin4
  N10: ATMEGA328.D1_(TX), J1.pin3, FTDI.pin5
  N11: ATMEGA328.D2, J1.pin4
  N12: ATMEGA328.D3_(PWM), J1.pin5
  N13: ATMEGA328.D4, J1.pin6
  N14: ATMEGA328.XLAT1, J1.pin9, XTAL1.pin_0, C1.1
  N15: ATMEGA328.XLAT2, J1.pin10, XTAL1.pin_1, C2.0
  N16: ATMEGA328.D5_(PWM), J1.pin11
  N17: ATMEGA328.D6_(PWM), J1.pin12
  N18: ATMEGA328.D7, J1.pin13
  N19: ATMEGA328.D8, J1.pin14
  N20: ATMEGA328.D9_(PWM), J2.pin14
  N21: ATMEGA328.D10_(PWM), J2.pin13
  N22: ATMEGA328.AREF, J2.pin8, C5.1
  N23: ATMEGA328.A0, J2.pin6
  N24: ATMEGA328.A1, J2.pin5
  N25: ATMEGA328.A2, J2.pin4
  N26: ATMEGA328.A3, J2.pin3
  N27: ATMEGA328.A4, J2.pin2
  N28: ATMEGA328.A5, J2.pin1
  N29: R1.Pin_0, 10k<>120.pin1
  N30: R2.Pin_0, 10k<>120.pin3
  N31: HB.anode, R5.Pin_1
  N32: ERR.anode, R4.Pin_1
  N33: PRG.anode, R3.Pin_1
  N34: C3.0, J5.pin2
  N35: C4.0, C4<>dir.pin3
  N36: FTDI.pin6, C6.1
  N37: PWR.anode, R6.Pin_1

notes:
  Arduino ISP
  v1/19.4.12
  <
  <-<-<
