# Fritzing sketch id488_ardunio_keyboard_shield_0 (saved by Fritzing 0.9.0b)
circuit board: 6.88566cm x 5.36311cm
breadboards: 1

parts:
  BTN-B = Pushbutton [package="[THT]"]
  BTN-A = Pushbutton [package="[THT]"]
  BTN-G = Pushbutton [package="[THT]"]
  BTN-F = Pushbutton [package="[THT]"]
  BTN-E = Pushbutton [package="[THT]"]
  BTN-D = Pushbutton [package="[THT]"]
  BTN-C = Pushbutton [package="[THT]"]
  BTN-Bb = Pushbutton [package="[THT]"]
  BTN-Ab = Pushbutton [package="[THT]"]
  BTN-Gb = Pushbutton [package="[THT]"]
  BTN-Eb = Pushbutton [package="[THT]"]
  BTN-Db = Pushbutton [package="[THT]"]
  R1 = Resistor [tolerance=±5% resistance=220 package=THT]
  R2 = Resistor [tolerance=±5% resistance=220 package=THT]
  R3 = Resistor [tolerance=±5% resistance=220 package=THT]
  R5 = Resistor [tolerance=±5% resistance=220 package=THT]
  R6 = Resistor [tolerance=±5% resistance=220 package=THT]
  R7 = Resistor [tolerance=±5% resistance=220 package=THT]
  R8 = Resistor [tolerance=±5% resistance=220 package=THT]
  R9 = Resistor [tolerance=±5% resistance=220 package=THT]
  R10 = Resistor [tolerance=±5% resistance=220 package=THT]
  R11 = Resistor [tolerance=±5% resistance=220 package=THT]
  R12 = Resistor [tolerance=±5% resistance=220 package=THT]
  Speaker = Piezo Speaker
  R4 = Resistor [tolerance=±5% resistance=220 package=THT]
  J3 = female pin header, 8 pins [form="♀ (female)"]
  J2 = female pin header, 8 pins [form="♀ (female)"]
  J4 = female pin header, 6 pins [form="♀ (female)"]  # not connected
  J5 = female pin header, 8 pins [form="♀ (female)"]  # not connected

nets (from the schematic view):
  N1: BTN-B.Pin_1, BTN-B.Pin_2, BTN-Bb.Pin_1, BTN-Bb.Pin_2
  N2: BTN-B.Pin_3, BTN-B.Pin_4, R1.Pin_0
  N3: BTN-A.Pin_1, BTN-A.Pin_2, BTN-Ab.Pin_1, BTN-Ab.Pin_2, Speaker.pin1
  N4: BTN-A.Pin_3, BTN-A.Pin_4, R2.Pin_1, J2.pin6
  N5: BTN-G.Pin_1, BTN-G.Pin_2, BTN-Gb.Pin_1, BTN-Gb.Pin_2
  N6: BTN-G.Pin_3, BTN-G.Pin_4, R3.Pin_1, J3.pin1
  N7: BTN-F.Pin_1, BTN-F.Pin_2, BTN-E.Pin_1, BTN-E.Pin_2, BTN-Eb.Pin_1, BTN-Eb.Pin_2
  N8: BTN-F.Pin_3, BTN-F.Pin_4, R4.Pin_1, J3.pin3
  N9: BTN-E.Pin_3, BTN-E.Pin_4, R5.Pin_1, J3.pin4
  N10: BTN-D.Pin_1, BTN-D.Pin_2, BTN-C.Pin_1, BTN-C.Pin_2, BTN-Db.Pin_1, BTN-Db.Pin_2
  N11: BTN-D.Pin_3, BTN-D.Pin_4, R6.Pin_1, J3.pin6
  N12: BTN-C.Pin_3, BTN-C.Pin_4, R7.Pin_1, J3.pin8
  N13: BTN-Bb.Pin_3, BTN-Bb.Pin_4
  N14: BTN-Ab.Pin_3, BTN-Ab.Pin_4, R9.Pin_0, J2.pin8
  N15: BTN-Gb.Pin_3, BTN-Gb.Pin_4, R10.Pin_0, J3.pin2
  N16: BTN-Eb.Pin_3, BTN-Eb.Pin_4, R11.Pin_0, J3.pin5
  N17: BTN-Db.Pin_3, BTN-Db.Pin_4, R12.Pin_0, J3.pin7
  N18: R1.Pin_1, J2.pin4
  N19: R2.Pin_0, R3.Pin_0, R5.Pin_0, R6.Pin_0, R7.Pin_0, R8.Pin_1, R9.Pin_1, R10.Pin_1, R11.Pin_1, R12.Pin_1, R4.Pin_0
  N20: R8.Pin_0, J2.pin5
  N21: Speaker.pin2, J2.pin7

notes:
  nobulb
  rev 1.0
  nobulb.com/project/keyboard-shield
  ----
  - --
  ---
