# Fritzing sketch id4894_powerdivider (saved by Fritzing 0.6.5b)
breadboards: 1

parts:
  Arduino1 = Arduino
  R2 = Resistor [tolerance=±5% resistance=4.7k package=THT]
  R1 = Resistor [tolerance=±5% resistance=10k package=THT]
  J1 = Screw terminal - 2 pins [package=THT]

nets:
  N1: Arduino1.GND, R2.Pin_1, J1.pin2
  N2: Arduino1.A0, R2.Pin_0, R1.Pin_1
  N3: R1.Pin_0, J1.pin1
