# Fritzing sketch id4899_regulators_+_RF (saved by Fritzing 0.9.3b)
circuit board: 8.46667cm x 5.64444cm
breadboards: 1

parts:
  U2 = Voltage Regulator - 3.3V [package="TO220 [THT]"]
  U3 = Voltage Regulator - 3.3V [package="TO220 [THT]"]
  IC1 = Voltage Regulator [package=78xxl]
  IC2 = Voltage Regulator [package=78xxl]
  C1 = Electrolytic Capacitor [capacitance=10μF voltage=50V package="0605 [SMD, electrolytic]"]
  C2 = Electrolytic Capacitor [capacitance=10μF voltage=50V package="0605 [SMD, electrolytic]"]
  C3 = Tantalum Capacitor [capacitance=10pF voltage=50V package="B 3528 [SMD, tantalum]"]
  C4 = Tantalum Capacitor [capacitance=10pF voltage=50V package="B 3528 [SMD, tantalum]"]
  Componente1 = NRF24L01+ Breakout Board
  Componente2 = NRF24L01+ Breakout Board
  Componente3 = Arduino Uno (Rev3) - ICSP
  Componente4 = Arduino Uno (Rev3) - ICSP
  U4 = LIPO-1000mAh [package=lipo-1000]

nets:
  N1: U2.input_voltage, IC2.OUT, C4.+, Componente4.5V
  GND: U2.GND, U3.GND, IC1.GND, IC2.GND, C1.-, C2.-, C3.-, C4.-, U4.+
  N2: U2.output_voltage, Componente1.VCC
  N3: U3.input_voltage, IC1.OUT, C3.+, Componente3.5V
  N4: U3.output_voltage, Componente2.VCC
  N5: IC1.IN, IC2.IN, C1.+, C2.+, U4.-
  GND_2: Componente1.GND, Componente4.GND
  N6: Componente1.CE, Componente4.D7
  N7: Componente1.CS, Componente4.D8
  N8: Componente1.SCK, Componente4.D13/SCK
  N9: Componente1.MOSI, Componente4.D11_PWM/MOSI
  N10: Componente1.MISO, Componente4.D12/MISO
  GND_3: Componente2.GND, Componente3.GND
  N11: Componente2.CE, Componente3.D7
  N12: Componente2.CS, Componente3.D8
  N13: Componente2.SCK, Componente3.ICSP_SCK, Componente3.D13/SCK
  N14: Componente2.MOSI, Componente3.D11_PWM/MOSI
  N15: Componente2.MISO, Componente3.ICSP_MISO, Componente3.D12/MISO
