# Fritzing sketch id489_Circuit_03_0 (saved by Fritzing 0.9.3b)
breadboards: 1

parts:
  Part1 = Arduino Uno (Rev3)
  R1 = Resistor [tolerance=±5% resistance=220 package=THT]
  Q1 = PNP-Transistor [package="TO92 [THT]"]
  M1 = DC Motor
  D1 = Rectifier Diode [part_number=1N4001 package="300 mil [THT]"]

nets:
  N1: Part1.D9_PWM, R1.Pin_1
  N2: Part1.5V, M1.pin_1, D1.cathode
  N3: Part1.GND, Q1.C
  N4: R1.Pin_0, Q1.B
  N5: Q1.E, M1.pin_2, D1.anode
