# Fritzing sketch id48_MicDiscoLights_0 (saved by Fritzing 0.9.3b)
breadboards: 1

parts:
  1Sheeld1 = 1Sheeld
  Part1 = Arduino Uno (Rev3)  # not connected
  LED1 = LED - 5mm [color="Red (633nm)" package="5 mm [THT]"]
  LED2 = LED - 5mm [color="Green (570nm)" package="5 mm [THT]"]
  LED3 = LED - 5mm [color="Yellow (595nm)" package="5 mm [THT]"]

nets:
  N1: 1Sheeld1.connector12, LED3.cathode
  N2: 1Sheeld1.connector13, LED2.cathode
  N3: 1Sheeld1.connector14, LED1.cathode
  N4: 1Sheeld1.connector27, LED1.anode, LED2.anode, LED3.anode
