# Fritzing sketch id491_Arduino_KnightRider___Photo_Resistor_0 (saved by Fritzing 0.9.2b)
breadboards: 1

parts:
  Part1 = Arduino Uno (Rev3)
  LED1 = LED - 5mm [color="Red (633nm)" package="5 mm [THT]"]
  LED2 = LED - 5mm [color="Red (633nm)" package="5 mm [THT]"]
  LED3 = LED - 5mm [color="Red (633nm)" package="5 mm [THT]"]
  LED4 = LED - 5mm [color="Red (633nm)" package="5 mm [THT]"]
  LED5 = LED - 5mm [color="Red (633nm)" package="5 mm [THT]"]
  LED6 = LED - 5mm [color="Red (633nm)" package="5 mm [THT]"]
  R1 = Resistor [tolerance=±5% resistance=220 package=THT]
  R2 = Resistor [tolerance=±5% resistance=220 package=THT]
  R3 = Resistor [tolerance=±5% resistance=220 package=THT]
  R4 = Resistor [tolerance=±5% resistance=220 package=THT]
  R5 = Resistor [tolerance=±5% resistance=220 package=THT]
  R6 = Resistor [tolerance=±5% resistance=220 package=THT]
  R8 = Resistor [tolerance=±5% resistance=220 package=THT]
  R9 = PHOTOCELL [package=photocell-kit]

nets:
  N1: Part1.A0, R8.Pin_1, R9.P$1
  N2: Part1.GND, LED1.cathode, LED2.cathode, LED3.cathode, LED4.cathode, LED5.cathode, LED6.cathode, R8.Pin_0
  N3: Part1.D2, R1.Pin_0
  N4: Part1.D3_PWM, R2.Pin_0
  N5: Part1.D4, R3.Pin_0
  N6: Part1.D5_PWM, R4.Pin_0
  N7: Part1.D6_PWM, R5.Pin_0
  N8: Part1.D7, R6.Pin_0
  N9: Part1.5V, R9.P$2
  N10: LED1.anode, R1.Pin_1
  N11: LED2.anode, R2.Pin_1
  N12: LED3.anode, R3.Pin_1
  N13: LED4.anode, R4.Pin_1
  N14: LED5.anode, R5.Pin_1
  N15: LED6.anode, R6.Pin_1

notes:
  Arduino Knightrider - Photo Resistor Controlled
  By Felix Ossa
  Modified from "Potentiometer controlling Knight Rider" by Pete Hawkes
  Try covering the Photo Resistor
  When the resistor is expossed to the maximum amount of light, the LED connected to pin 7 will be active (blink).
  As the sensor recives less light, the LEDs will be active in descending order.
  When the Photo Resistor does not sense light, the LED connected to Pin 2 will be active (blink).
