# Fritzing sketch id493_lamp_0 (saved by Fritzing 0.9.2b)
breadboards: 1

parts:
  Part1 = Arduino Uno (Rev3)
  R1 = Resistor [tolerance=±5% resistance=220 package=THT]
  R2 = Resistor [tolerance=±5% resistance=220 package=THT]
  R3 = Resistor [tolerance=±5% resistance=220 package=THT]
  LED1 = RGB LED (com. cathode, rgb) [package="5 mm [THT]"]
  R4 = Resistor [tolerance=±5% resistance=10k package=THT]
  R5 = Resistor [tolerance=±5% resistance=10k package=THT]
  R6 = Resistor [tolerance=±5% resistance=10k package=THT]
  R7 = Photocell (LDR) [package=THT]
  R8 = Photocell (LDR) [package=THT]
  R9 = Photocell (LDR) [package=THT]

nets:
  N1: Part1.A0, R4.Pin_1, R7.pin_0
  N2: Part1.A1, R5.Pin_1, R8.pin_0
  N3: Part1.A2, R6.Pin_1, R9.pin_0
  N4: Part1.D9_PWM, R3.Pin_0
  N5: Part1.D10_PWM/SS, R2.Pin_0
  N6: Part1.D11_PWM/MOSI, R1.Pin_1
  N7: Part1.5V, R7.pin_1, R8.pin_1, R9.pin_1
  N8: Part1.GND, LED1.common_cathode, R4.Pin_0, R5.Pin_0, R6.Pin_0
  N9: R1.Pin_0, LED1.red_anode
  N10: R2.Pin_1, LED1.green_anode
  N11: R3.Pin_1, LED1.blue_anode
