# Fritzing sketch id494_ArduinoFlashTriggerr_0 (saved by Fritzing 0.7.7b)
breadboards: 1

parts:
  Matic_Subelj_DSLR_Flash_Trigger = Arduino
  Flash_Trigger = female pin header, 2 pins [form="♀ (female)"]
  R1 = Resistor [tolerance=±5% resistance=10k package=THT]
  R3 = Resistor [tolerance=±5% resistance=220 package=THT]
  Laser_Power = female pin header, 2 pins [form="♀ (female)"]
  R4 = Resistor [tolerance=±5% resistance=100 package=THT]
  On-Off = Pushbutton [package=THT]
  Sound_or_Laser = Pushbutton [package=THT]
  R5 = Resistor [tolerance=±5% resistance=2.2k package=THT]
  R6 = Resistor [tolerance=±5% resistance=2.2k package=THT]
  MOC_3021 = Optocoupler [package=THT]
  R8 = Resistor [tolerance=±5% resistance=220 package=THT]
  FlashPin = female pin header, 2 pins [form="♀ (female)"]
  Laser_Thrashhold = Rotary Potentiometer (Small) [maximum_resistance=10kΩ]
  Sound_Thrashhold = Rotary Potentiometer (Small) [maximum_resistance=10kΩ]
  D1 = Rectifier Diode [part_number=1N4001 package="300 mil [THT]"]
  SoundPin = female pin header, 2 pins [form="♀ (female)"]
  Status_LED = female pin header, 2 pins [form="♀ (female)"]

nets:
  N1: Matic_Subelj_DSLR_Flash_Trigger.GND, Matic_Subelj_DSLR_Flash_Trigger.D11, Matic_Subelj_DSLR_Flash_Trigger.D3, R1.Pin_1, R3.Pin_1, R5.Pin_0, R6.Pin_0, R8.Pin_1, Laser_Thrashhold.leg1, Sound_Thrashhold.leg1, D1.anode, SoundPin.pin1, Status_LED.pin2
  N2: Matic_Subelj_DSLR_Flash_Trigger.D13, Status_LED.pin1
  N3: Matic_Subelj_DSLR_Flash_Trigger.D5, R4.Pin_1
  N4: Matic_Subelj_DSLR_Flash_Trigger.D4, MOC_3021.Pin_1
  N5: Matic_Subelj_DSLR_Flash_Trigger.+5V, Flash_Trigger.pin1, On-Off.leg1, Sound_or_Laser.leg1, Laser_Thrashhold.leg2, Sound_Thrashhold.leg2
  N6: Matic_Subelj_DSLR_Flash_Trigger.A1, D1.cathode, SoundPin.pin2
  N7: Matic_Subelj_DSLR_Flash_Trigger.A2, Laser_Thrashhold.wiper
  N8: Matic_Subelj_DSLR_Flash_Trigger.A3, Sound_Thrashhold.wiper
  N9: Matic_Subelj_DSLR_Flash_Trigger.A5, Flash_Trigger.pin2, R1.Pin_0
  N10: R3.Pin_0, Laser_Power.pin2
  N11: Laser_Power.pin1, R4.Pin_0
  N12: On-Off.leg0, R5.Pin_1
  N13: Sound_or_Laser.leg0, R6.Pin_1
  N14: MOC_3021.Pin_2, R8.Pin_0
  N15: MOC_3021.Pin_4, FlashPin.pin2
  N16: MOC_3021.Pin_5, FlashPin.pin1
