# Fritzing sketch id495_LCD_0 (saved by Fritzing 0.9.3b)
breadboards: 1

parts:
  Part1 = Arduino Uno (Rev3)
  U1 = LCD-16X2 [package=lcd-16x2]  # not connected
  RE1 = Rotary Encoder [package=THT]

nets:
  N1: Part1.GND, RE1.EncoderPinB
  N2: Part1.5V, RE1.EncoderPinA
