# Fritzing sketch id498_Untitled_Sketch_0 (saved by Fritzing 0.9.0b)
breadboards: 2

parts:
  LCD1 = LCD screen
  Part1 = Arduino Leonardo (Rev3b)
  S1 = Pushbutton [package="[THT]"]
  S2 = Pushbutton [package="[THT]"]
  S3 = Pushbutton [package="[THT]"]
  S4 = Pushbutton [package="[THT]"]
  R1 = Resistor [tolerance=±5% resistance=220 package=THT]
  R2 = Rotary Potentiometer (Small) [maximum_resistance=100kΩ package=THT]

nets:
  VSS: LCD1.VSS, LCD1.R/W, Part1.GND, S1.Pin_1, S1.Pin_2, S2.Pin_1, S2.Pin_2, S3.Pin_1, S3.Pin_2, S4.Pin_1, S4.Pin_2, R1.Pin_1, R2.leg1
  VDD: LCD1.VDD, LCD1.LED+, Part1.5V, R2.leg2
  N1: LCD1.V0, R2.wiper
  N2: LCD1.RS, Part1.D7
  N3: LCD1.E, Part1.D6_PWM/A7
  N4: LCD1.DB4, Part1.D5_PWM
  N5: LCD1.DB5, Part1.D4/A6
  N6: LCD1.DB6, Part1.D3_PWM/SCL
  N7: LCD1.DB7, Part1.D2/SDA
  N8: LCD1.LED-, R1.Pin_0
  N9: Part1.D8/A8, S4.Pin_3, S4.Pin_4
  N10: Part1.D9_PWM/A9, S3.Pin_3, S3.Pin_4
  N11: Part1.D10_PWM/A10, S1.Pin_3, S1.Pin_4
  N12: Part1.D11_PWM, S2.Pin_3, S2.Pin_4
