# Fritzing sketch id49_blink_led_0 (saved by Fritzing 0.9.3b)
breadboards: 1

parts:
  パーツ1 = Arduino Leonardo (Rev3b)
  LED1 = LED - 5mm [color="Red (633nm)" package="5 mm [THT]"]

nets:
  N1: パーツ1.GND, LED1.anode
  N2: パーツ1.D12/A11, LED1.cathode

notes:
  配線の色によって挙動が
  変わることはありません。
