# Fritzing sketch id4_Knop_Kovb_0 (saved by Fritzing 0.9.3b)
breadboards: 2

parts:
  Часть2 = Arduino Nano (Rev3.0)
  DI1 = 7-Segment LED Display [package=THT]
  S1 = Pushbutton [package="[THT]"]
  S2 = Pushbutton [package="[THT]"]
  S3 = Pushbutton [package="[THT]"]
  J1 = Piezo Speaker
  R1 = Resistor [tolerance=±5% resistance=10k package=THT]
  R2 = Resistor [tolerance=±5% resistance=10k package=THT]
  R4 = Resistor [tolerance=±5% resistance=10k package=THT]
  R5 = Resistor [tolerance=±5% resistance=10k package=THT]
  R6 = Resistor [tolerance=±5% resistance=10k package=THT]
  R7 = Resistor [tolerance=±5% resistance=10k package=THT]
  R8 = Resistor [tolerance=±5% resistance=10k package=THT]
  R9 = Resistor [tolerance=±5% resistance=10k package=THT]
  R10 = Resistor [tolerance=±5% resistance=10k package=THT]
  R11 = Resistor [tolerance=±5% resistance=10k package=THT]
  LED1 = LED - 5mm [color="Red (633nm)" package="5 mm [THT]"]
  LED2 = LED - 5mm [color="Orange (620nm)" package="5 mm [THT]"]
  R12 = Resistor [tolerance=±5% resistance=220 package=THT]
  R13 = Resistor [tolerance=±5% resistance=220 package=THT]
  R14 = Resistor [tolerance=±5% resistance=10k package=THT]

nets:
  N1: Часть2.GND, J1.pin1, R1.Pin_1, R2.Pin_1, R4.Pin_1, R5.Pin_1, R6.Pin_1, R7.Pin_1, R12.Pin_1, R13.Pin_1, R14.Pin_0
  N2: Часть2.D2, DI1.cathodeDP, R7.Pin_0
  N3: Часть2.D3, DI1.cathodeC, R6.Pin_0
  N4: Часть2.D4, DI1.cathodeD, R5.Pin_0
  N5: Часть2.D5, DI1.cathodeE, R4.Pin_0
  N6: Часть2.D6, DI1.cathodeB, R8.Pin_1
  N7: Часть2.D7, DI1.cathodeA, R11.Pin_1
  N8: Часть2.D8, DI1.cathodeF, R9.Pin_1
  N9: Часть2.D9, DI1.cathodeG, R10.Pin_1
  N10: Часть2.D10, LED2.anode
  N11: Часть2.D11/MOSI, LED1.anode
  N12: Часть2.D12/MISO, S1.Pin_3, S1.Pin_4, R1.Pin_0
  N13: Часть2.5V, DI1.commAnode#2, S1.Pin_1, S1.Pin_2, S2.Pin_3, S2.Pin_4
  N14: Часть2.A1, S3.Pin_3, S3.Pin_4
  N15: Часть2.A0, J1.pin2
  N16: Часть2.D13/SCK, S2.Pin_1, S2.Pin_2, R2.Pin_0
  N17: S3.Pin_1, S3.Pin_2, R14.Pin_1
  N18: R8.Pin_0, R9.Pin_0, R10.Pin_0, R11.Pin_0
  N19: LED1.cathode, R12.Pin_0
  N20: LED2.cathode, R13.Pin_0

notes:
  Игрок 2
  Игрок 1
  220оМ
  10КоМ
