# Fritzing sketch id5009_Arduino_Serial_Communication (saved by Fritzing 0.6.5b)
breadboards: 1

parts:
  R1 = Resistor [tolerance=±5% resistance=220 package=THT]
  LED1 = LED - 5mm [color="Red (633nm)" package="5 mm [THT]"]
  R2 = Resistor [tolerance=±5% resistance=10k package=THT]
  S1 = Toggle Switch [package=THT]
  Arduino1 = Arduino
  APC1 = APC220
  ANT1 = Antenna  # not connected

nets:
  N1: R1.Pin_0, LED1.cathode
  N2: R1.Pin_1, R2.Pin_1, Arduino1.GND, APC1.connector0
  N3: LED1.anode, Arduino1.D2
  N4: R2.Pin_0, S1.L2, Arduino1.D3
  N5: S1.COM, Arduino1.+5V, APC1.connector1
  N6: Arduino1.D1TX, APC1.connector2
  N7: Arduino1.D0RX, APC1.connector3
