# Fritzing sketch id500_wyswietlacz_plytka_0 (saved by Fritzing 0.9.3b)
circuit board: 6.88566cm x 5.36311cm
breadboards: 1

parts:
  LCD = LCD screen  # not connected
  Jasność = Trimmer Potentiometer [maximum_resistance=1kΩ package=THT]
  Kontrast = Trimmer Potentiometer [maximum_resistance=5kΩ package=THT]
  Arduino = Arduino Uno (Rev3)  # not connected
  J1 = male pin header, 8 pins [form="♂ (male)"]
  J2 = male pin header, 6 pins [form="♂ (male)"]  # not connected
  J3 = male pin header, 10 pins [form="♂ (male)"]
  J4 = male pin header, 8 pins [form="♂ (male)"]
  J5 = rounded female pin header, 16 pins [form="♀ (female rounded)"]

nets:
  N1: Jasność.leg1, Kontrast.leg1, J1.pin5, J5.pin2
  N2: Jasność.wiper, J5.pin15
  N3: Jasność.leg2, Kontrast.leg2, J1.pin6, J1.pin7, J3.pin4, J5.pin1, J5.pin5, J5.pin16
  N4: Kontrast.wiper, J5.pin3
  N5: J3.pin6, J5.pin4
  N6: J3.pin7, J5.pin6
  N7: J4.pin3, J5.pin11
  N8: J4.pin4, J5.pin12
  N9: J4.pin5, J5.pin13
  N10: J4.pin6, J5.pin14
