# Fritzing sketch id5016_Wiring_RJ45_Shield_Wide (saved by Fritzing 0.5.2b)

parts:
  Wiring1 = Wiring
  Part1 = RJ45
  Part1_2 = RJ45
  Part1_3 = RJ45
  Part1_4 = RJ45
  Part1_5 = RJ45
  Part2 = RJ45
  Part1_6 = RJ45
  Part1_7 = RJ45
  J1 = female pin header, 2 pins [form="♀ (female)"]
  J2 = female pin header, 8 pins [form="♀ (female)"]
  Part3 = RJ45

nets:
  N1: Wiring1.D0, Part1.connector0
  N2: Wiring1.D1, Part1.connector2
  N3: Wiring1.D2, Part1.connector1
  N4: Wiring1.D3, Part1.connector3
  N5: Wiring1.D4, Part1.connector5
  N6: Wiring1.D5, Part1.connector7
  N7: Wiring1.D6, Part1.connector4
  N8: Wiring1.D7, Part1.connector6
  N9: Wiring1.D8, Part1_2.connector0
  N10: Wiring1.D9, Part1_2.connector2
  N11: Wiring1.D10, Part1_2.connector1
  N12: Wiring1.D11, Part1_2.connector3
  N13: Wiring1.D12, Part1_2.connector5
  N14: Wiring1.D13, Part1_2.connector7
  N15: Wiring1.D14, Part1_2.connector4
  N16: Wiring1.D15, Part1_2.connector6
  N17: Wiring1.D16, Part1_3.connector0
  N18: Wiring1.D17, Part1_3.connector2
  N19: Wiring1.D18, Part1_3.connector1
  N20: Wiring1.D19, Part1_3.connector3
  N21: Wiring1.D20, Part1_3.connector5
  N22: Wiring1.D21, Part1_3.connector7
  N23: Wiring1.D22, Part1_3.connector4
  N24: Wiring1.D23, Part1_3.connector6
  N25: Wiring1.VCC, Part2.connector0, Part2.connector1, J2.pin4, J2.pin6, Part3.connector4, Part3.connector6
  N26: Wiring1.GND, Part2.connector2, Part2.connector3, Part2.connector4, Part2.connector5, J2.pin1, J2.pin3, J2.pin5, Part3.connector2, Part3.connector3, Part3.connector5
  N27: Wiring1.Vin, Part2.connector6, Part2.connector7
  N28: Wiring1.PWM5, Part1_6.connector1
  N29: Wiring1.PWM4, Part1_6.connector3
  N30: Wiring1.PWM3, Part1_6.connector5
  N31: Wiring1.PWM2, Part1_6.connector7
  N32: Wiring1.PWM1, Part1_6.connector4
  N33: Wiring1.PWM0, Part1_6.connector6
  N34: Wiring1.A7, Part1_4.connector0
  N35: Wiring1.A6, Part1_4.connector2
  N36: Wiring1.A5, Part1_4.connector1
  N37: Wiring1.A4, Part1_4.connector3
  N38: Wiring1.A3, Part1_4.connector5
  N39: Wiring1.A2, Part1_4.connector7
  N40: Wiring1.A1, Part1_4.connector4
  N41: Wiring1.A0, Part1_4.connector6
  N42: Wiring1.D39, Part1_5.connector0
  N43: Wiring1.D38, Part1_5.connector2
  N44: Wiring1.D37, Part1_5.connector1
  N45: Wiring1.D36, Part1_5.connector3
  N46: Wiring1.D35, Part1_5.connector5
  N47: Wiring1.D34, Part1_5.connector7
  N48: Wiring1.D33, Part1_5.connector4
  N49: Wiring1.D32, Part1_5.connector6
  N50: Wiring1.D31, Part1_7.connector0
  N51: Wiring1.D30, Part1_7.connector2
  N52: Wiring1.D29, Part1_7.connector1
  N53: Wiring1.D28, Part1_7.connector3
  N54: Wiring1.D27, Part1_7.connector5
  N55: Wiring1.D26, Part1_7.connector7
  N56: Wiring1.D25, Part1_7.connector4
  N57: Wiring1.D24, Part1_7.connector6
  N58: Wiring1.D50, J2.pin8, Part3.connector0
  N59: Wiring1.D49, J2.pin7, Part3.connector1
  N60: Wiring1.AREF, J2.pin2, Part3.connector7
  N61: Part1_6.connector0, J1.pin2
  N62: Part1_6.connector2, J1.pin1

notes:
  Port 0
  Port 1
  Port 2
  VCC
  VIN
  GND
  ARef
  49
  50
  Pwr Bus
  16 - 23
  8 - 15
  0 - 7
  Port 3
  Port 4
  Analogue In
  PWM
  24 - 31
  32 - 39
  0 - 5
  Pwr Bus 2
  RJ-45
  Shield
  Wide Edition
