# Fritzing sketch id502_Untitled_Sketch_0 (saved by Fritzing 0.9.0b)
breadboards: 1

parts:
  LCD1 = LCD screen
  R1 = Rotary Potentiometer (Small) [maximum_resistance=100kΩ package=THT]
  S1 = Pushbutton [package="[THT]"]
  S2 = Pushbutton [package="[THT]"]
  Part1 = Arduino Leonardo (Rev3b)
  R2 = Resistor [tolerance=±5% resistance=220 package=THT]

nets:
  VSS: LCD1.VSS, LCD1.R/W, LCD1.LED-, R1.leg2, S1.Pin_3, S1.Pin_4, S2.Pin_3, S2.Pin_4, Part1.GND
  VDD: LCD1.VDD, R1.leg1, Part1.5V, R2.Pin_1
  N1: LCD1.V0, R1.wiper
  N2: LCD1.RS, Part1.D7
  N3: LCD1.E, Part1.D6_PWM/A7
  N4: LCD1.DB4, Part1.D5_PWM
  N5: LCD1.DB5, Part1.D4/A6
  N6: LCD1.DB6, Part1.D3_PWM/SCL
  N7: LCD1.DB7, Part1.D2/SDA
  N8: LCD1.LED+, R2.Pin_0
  N9: S1.Pin_1, S1.Pin_2, Part1.D8/A8
  N10: S2.Pin_1, S2.Pin_2, Part1.D9_PWM/A9
