# Fritzing sketch id503_LCD_0 (saved by Fritzing 0.9.2b)
breadboards: 1

parts:
  Part1 = Arduino Uno (Rev3)
  U1 = LCD-16X2 [package=lcd-16x2]
  R1 = Resistor [tolerance=±5% resistance=220 package="1206 [SMD]"]
  R2 = Trimmer Potentiometer [maximum_resistance=10kΩ package=THT]

nets:
  N1: Part1.D12/MISO, U1.RS
  N2: Part1.D2, U1.DB7
  N3: Part1.D3_PWM, U1.DB6
  N4: Part1.D4, U1.DB5
  N5: Part1.D5_PWM, U1.DB4
  5V: Part1.5V, U1.VDD, R1.Pin_1, R2.leg2
  GND: Part1.GND, U1.VSS, U1.K, R2.leg1
  N6: U1.VO, R2.wiper
  N7: U1.A, R1.Pin_0
