# Fritzing sketch id505_Arduino_LED_Light_Chase_(Diwali_2015)_0 (saved by Fritzing 0.9.2b)
breadboards: 1

parts:
  Part1 = Arduino Uno (Rev3)
  LED1 = LED - 5mm [color="Red (633nm)" package="5 mm [THT]"]
  LED2 = LED - 5mm [color="Orange (620nm)" package="5 mm [THT]"]
  LED3 = LED - 5mm [color="Yellow (592nm)" package="5 mm [THT]"]
  LED4 = LED - 5mm [color="Green (565nm)" package="5 mm [THT]"]
  LED5 = LED - 5mm [color="Blue (505nm)" package="5 mm [THT]"]
  LED6 = LED - 5mm [color="Red (633nm)" package="5 mm [THT]"]
  LED7 = LED - 5mm [color="Orange (612nm)" package="5 mm [THT]"]
  LED8 = LED - 5mm [color="Yellow (595nm)" package="5 mm [THT]"]
  LED9 = LED - 5mm [color="Green (565nm)" package="5 mm [THT]"]
  LED10 = LED - 5mm [color="Blue (525nm)" package="5 mm [THT]"]
  R1 = Resistor [tolerance=±5% resistance=220 package=THT]
  R2 = Resistor [tolerance=±5% resistance=220 package=THT]
  R3 = Resistor [tolerance=±5% resistance=220 package=THT]
  R4 = Resistor [tolerance=±5% resistance=220 package=THT]
  R5 = Resistor [tolerance=±5% resistance=220 package=THT]
  R6 = Resistor [tolerance=±5% resistance=220 package=THT]
  R7 = Resistor [tolerance=±5% resistance=220 package=THT]
  R8 = Resistor [tolerance=±5% resistance=220 package=THT]
  R9 = Resistor [tolerance=±5% resistance=220 package=THT]
  R10 = Resistor [tolerance=±5% resistance=220 package=THT]
  R11 = Resistor [tolerance=±5% resistance=10k package=THT]

nets:
  N1: Part1.D8, LED8.anode, R8.Pin_0, R8.Pin_1
  N2: Part1.D9_PWM, LED9.anode, R9.Pin_0, R9.Pin_1
  N3: Part1.D10_PWM/SS, LED10.anode, R10.Pin_0, R10.Pin_1
  N4: Part1.GND, R11.Pin_0
  N5: Part1.D1/TX, LED1.anode, R1.Pin_0, R1.Pin_1
  N6: Part1.D2, LED2.anode, R2.Pin_0, R2.Pin_1
  N7: Part1.D3_PWM, LED3.anode, R3.Pin_0, R3.Pin_1
  N8: Part1.D4, LED4.anode, R4.Pin_0, R4.Pin_1
  N9: Part1.D5_PWM, LED5.anode, R5.Pin_0, R5.Pin_1
  N10: Part1.D6_PWM, LED6.anode, R6.Pin_0, R6.Pin_1
  N11: Part1.D7, LED7.anode, R7.Pin_0, R7.Pin_1
  N12: LED1.cathode, LED2.cathode, LED3.cathode, LED4.cathode, LED5.cathode, LED6.cathode, LED7.cathode, LED8.cathode, LED9.cathode, LED10.cathode, R11.Pin_1
