# Fritzing sketch id505_LCD_Temp (saved by Fritzing 0.4.2b)
breadboards: 1

parts:
  Arduino1 = Arduino
  LCD1 = LCD screen
  U1 = mystery part, 3 pins [chip_label=DS1820 spacing=300mil]
  R2 = Resistor [resistance=4.7 package=THT]
  R1 = Trimmer Potentiometer [package=THT]

nets:
  GND: Arduino1.GND, LCD1.VSS, LCD1.LED-, U1.pin1, R1.leg2
  N1: Arduino1.D12, LCD1.RS
  N2: Arduino1.D11, LCD1.R/W
  N3: Arduino1.D10, LCD1.E
  N4: Arduino1.D8, U1.pin2, R2.Pin_0
  N5: Arduino1.D5, LCD1.DB4
  N6: Arduino1.D4, LCD1.DB5
  N7: Arduino1.D3, LCD1.DB6
  N8: Arduino1.D2, LCD1.DB7
  +5V: Arduino1.+5V, LCD1.VDD, R2.Pin_1, R1.leg1
  N9: LCD1.V0, R1.wiper

notes:
  Термометр на Arduino с цифровым датчиком DS1820 и выводом на LCD дисплей WH1602B-NYG-CT
