# Fritzing sketch id506_ARDUINO_LED_LAMPEGGIANTE_0 (saved by Fritzing 0.9.3b)
circuit board: 8.46667cm x 5.64444cm
breadboards: 1

parts:
  VCC1 = Battery block 9V
  R1 = Resistor [tolerance=±5% resistance=220 package=THT]
  LED_1 = smd LED [color="Red (633nm)" package="0603 [SMD]"]
  ARDUINO_UNO = Arduino Uno (Rev3)

nets:
  N1: VCC1.-, LED_1.cathode, ARDUINO_UNO.GND
  N2: VCC1.+, ARDUINO_UNO.VIN
  N3: R1.Pin_0, ARDUINO_UNO.D8
  N4: R1.Pin_1, LED_1.anode
