# Fritzing sketch id5079_emf_detector (saved by Fritzing 0.6.3b)
breadboards: 1

parts:
  Arduino2 = Arduino
  DI1 = 7-Segment LED Display [package=THT]
  R1 = Resistor [tolerance=±5% resistance=220 package=THT]
  R2 = Resistor [tolerance=±5% resistance=220 package=THT]

nets:
  N1: Arduino2.D9, DI1.cathodeDP
  N2: Arduino2.D8, DI1.cathodeG
  N3: Arduino2.D7, DI1.cathodeF
  N4: Arduino2.D6, DI1.cathodeE
  N5: Arduino2.D5, DI1.cathodeD
  N6: Arduino2.D4, DI1.cathodeC
  N7: Arduino2.D3, DI1.cathodeB
  N8: Arduino2.D2, DI1.cathodeA
  N9: Arduino2.3V3, R1.Pin_0
  N10: Arduino2.A5, R2.Pin_1
  N11: DI1.commAnode#7, R1.Pin_1
