# Fritzing sketch id507_photoresistor_0 (saved by Fritzing 0.9.3b)
breadboards: 1

parts:
  Part1 = Arduino Uno (Rev3)
  LED1 = LED - 5mm [color="Red (633nm)" package="5 mm [THT]"]
  R1 = Resistor [tolerance=±5% resistance=330 package=THT]
  R2 = Resistor [tolerance=±5% resistance=10k package=THT]
  R3 = Photocell (LDR) [package=THT]

nets:
  N1: Part1.A0, R2.Pin_0, R3.pin_0
  N2: Part1.D9_PWM, LED1.anode
  N3: Part1.5V, R2.Pin_1
  N4: Part1.GND, R1.Pin_1, R3.pin_1
  N5: LED1.cathode, R1.Pin_0
