# Fritzing sketch id508_potentiometer_led_0 (saved by Fritzing 0.9.3b)
circuit board: 8.46667cm x 5.64444cm
breadboards: 1

parts:
  R1 = Rotary Potentiometer (Small) [maximum_resistance=100kΩ package=THT]
  LED1 = LED - 5mm [color="Yellow (592nm)" package="5 mm [THT]"]
  R2 = Resistor [tolerance=±5% resistance=220 package=THT]
  Part2 = Arduino Yun

nets:
  N1: R1.leg1, Part2.5V
  N2: R1.wiper, Part2.A2
  N3: R1.leg2, R2.Pin_1, Part2.GND
  N4: LED1.cathode, R2.Pin_0
  N5: LED1.anode, Part2.ICSP_SCK, Part2.D13/SCK
