# Fritzing sketch id509_led_lighting_effect_0 (saved by Fritzing 0.9.3b)
breadboards: 1

parts:
  Part1 = Arduino Uno (Rev3)
  LED1 = LED - 5mm [color="Red (633nm)" package="5 mm [THT]"]
  LED2 = LED - 5mm [color="Orange (620nm)" package="5 mm [THT]"]
  LED3 = LED - 5mm [color="Yellow (595nm)" package="5 mm [THT]"]
  LED4 = LED - 5mm [color="Green (570nm)" package="5 mm [THT]"]
  LED5 = LED - 5mm [color="White (6500K)" package="5 mm [THT]"]
  LED6 = LED - 5mm [color="Blue (505nm)" package="5 mm [THT]"]
  R1 = Resistor [tolerance=±5% resistance=1 package=THT]
  R2 = Resistor [tolerance=±5% resistance=1 package=THT]
  R3 = Resistor [tolerance=±5% resistance=1 package=THT]
  R4 = Resistor [tolerance=±5% resistance=1 package=THT]
  R5 = Resistor [tolerance=±5% resistance=1 package=THT]
  R6 = Resistor [tolerance=±5% resistance=1 package=THT]

nets:
  N1: Part1.D9_PWM, LED4.anode, R5.Pin_0, R5.Pin_1
  N2: Part1.D10_PWM/SS, LED5.anode, R4.Pin_0, R4.Pin_1
  N3: Part1.D11_PWM/MOSI, LED6.anode, R3.Pin_0, R3.Pin_1
  N4: Part1.D3_PWM, LED1.anode, R1.Pin_0, R1.Pin_1
  N5: Part1.D5_PWM, LED2.anode, R2.Pin_0, R2.Pin_1
  N6: Part1.D6_PWM, LED3.anode, R6.Pin_0, R6.Pin_1
  N7: Part1.GND, LED2.cathode, LED4.cathode, LED5.cathode
