# Fritzing sketch id50_Blink_2_0 (saved by Fritzing 0.8.7b)
breadboards: 1

parts:
  LED1 = LED - 5mm [color="Red (633nm)" package="5 mm [THT]"]
  LED2 = LED - 5mm [color="Green (570nm)" package="5 mm [THT]"]
  R1 = Resistor [tolerance=±5% resistance=220 package=THT]
  R2 = Resistor [tolerance=±5% resistance=220 package=THT]
  Part2 = Arduino Uno (Rev3)

nets:
  N1: LED1.cathode, LED2.cathode, Part2.GND
  N2: LED1.anode, R1.Pin_0
  N3: LED2.anode, R2.Pin_0
