# Fritzing sketch id510_ButtonBoxV2_0 (saved by Fritzing 0.9.2b)

parts:
  LED1 = LED - 5mm [color="Green (560nm)" package="5 mm [THT]"]
  LED2 = LED - 5mm [color="Orange (612nm)" package="5 mm [THT]"]  # not connected
  LED3 = LED - 5mm [color="Blue (470nm)" package="5 mm [THT]"]
  SW1 = prefix0000
  Bauteil1 = Arduino Leonardo (Rev3b)
  S1 = Momentary Switch [package=ksa_sealed_tac_switch]  # not connected
  S2 = Momentary Switch [package=ksa_sealed_tac_switch]  # not connected
  S3 = Momentary Switch [package=ksa_sealed_tac_switch]  # not connected
  S4 = Momentary Switch [package=ksa_sealed_tac_switch]
  S5 = SWITCH-SP3T [package=switch-sp3t-smd]  # not connected
  S6 = SWITCH-SP3T [package=switch-sp3t-smd]  # not connected
  S7 = SWITCH-SP3T [package=switch-sp3t-smd]
  S8 = SWITCH-SP3T [package=switch-sp3t-smd]
  S9 = Round Pushbutton  # not connected
  U1 = SWITCH_SPDT [package=kps-1290]  # not connected
  LED7 = LED - 5mm [color="Red (633nm)" package="5 mm [THT]"]  # not connected
  LED8 = LED - 5mm [color="Orange (612nm)" package="5 mm [THT]"]  # not connected
  LED9 = LED - 5mm [color="Blue (470nm)" package="5 mm [THT]"]
  LED10 = LED - 5mm [color="Green (560nm)" package="5 mm [THT]"]  # not connected
  LED11 = LED - 5mm [color="Red (633nm)" package="5 mm [THT]"]
  LED12 = LED - 5mm [color="Red (633nm)" package="5 mm [THT]"]  # not connected
  S10 = Pushbutton [package="[THT]"]  # not connected
  S11 = Pushbutton [package="[THT]"]
  LED13 = LED - 5mm [color="Red (633nm)" package="5 mm [THT]"]  # not connected
  LED14 = LED - 5mm [color="Blue (470nm)" package="5 mm [THT]"]
  SW4 = prefix0000
  LED15 = LED - 5mm [color="White (6500K)" package="5 mm [THT]"]  # not connected
  MIC1 = Microphone

nets:
  N1: LED1.anode, Bauteil1.A3
  N2: LED3.cathode, Bauteil1.GND, LED11.cathode, LED14.cathode
  N3: LED3.anode, Bauteil1.A1
  N4: SW1.connector1, Bauteil1.D2/SDA, S11.Pin_3, S11.Pin_4
  N5: SW1.connector3, SW1.connector4, Bauteil1.D7, S4.4
  N6: SW1.connector5, Bauteil1.D4/A6, SW4.connector1
  N7: Bauteil1.3V3, LED9.anode
  N8: Bauteil1.5V, LED11.anode
  N9: Bauteil1.A4, MIC1.pin2
  N10: Bauteil1.D8/A8, S7.1
  N11: S4.2, SW4.connector5
  N12: S7.2, S8.2
  N13: SW4.connector3, SW4.connector4

notes:
  USB-Port
  Power-Switch
  Headlight/Flashlight
  Engine Start / Screenshot
  4 x Rotary Switch
  4 x Push Button
  3 x LED
  with permanent LED on
  Button with permanen LED on
  Power-LED
  2 x Push Button with
  permanent LED on
  Vibration-Motor
  ButtonBoxV2
  by Markus Dörner 2016
