# Fritzing sketch id512_Untitled_Sketch_0 (saved by Fritzing 0.9.0b)
breadboards: 1

parts:
  R1 = Resistor [tolerance=±5% resistance=220 package=THT]
  R2 = Resistor [tolerance=±5% resistance=220 package=THT]
  R3 = Resistor [tolerance=±5% resistance=220 package=THT]
  R4 = Resistor [tolerance=±5% resistance=220 package=THT]
  R5 = Resistor [tolerance=±5% resistance=220 package=THT]
  R6 = Photocell (LDR) [package=THT]
  LED1 = LED - 5mm [color="Blue (525nm)" package="5 mm [THT]"]
  LED2 = LED - 5mm [color="Blue (525nm)" package="5 mm [THT]"]
  LED3 = LED - 5mm [color="Blue (525nm)" package="5 mm [THT]"]
  LED4 = LED - 5mm [color="Blue (525nm)" package="5 mm [THT]"]
  Part1 = Arduino Leonardo (Rev3b)

nets:
  N1: R1.Pin_0, Part1.D12/A11
  N2: R1.Pin_1, LED3.anode
  N3: R2.Pin_0, R6.pin_1, Part1.A0
  N4: R2.Pin_1, LED3.cathode, LED4.cathode, Part1.GND
  N5: R3.Pin_0, LED4.anode
  N6: R4.Pin_0, Part1.D11_PWM
  N7: R4.Pin_1, LED2.anode
  N8: R5.Pin_0, LED1.anode
  N9: R5.Pin_1, Part1.D10_PWM/A10
  N10: R6.pin_0, Part1.5V
  N11: LED1.cathode, LED2.cathode
