# Fritzing sketch id513_ArduinoLightSensor_0 (saved by Fritzing 0.9.1b)
breadboards: 1

parts:
  Part1 = Arduino Uno (Rev3)
  R1 = Resistor [tolerance=±20% resistance=220 package=THT]
  LED1 = LED - 5mm [color="Red (633nm)" package="5 mm [THT]"]

nets:
  N1: Part1.D13/SCK, R1.Pin_1
  N2: Part1.GND, LED1.cathode
  N3: R1.Pin_0, LED1.anode

notes:
  There is a TSL2561 Lux Sensor that goes to the left of this note.
  Yellow is connected to SCL.
  Black is connected to SDA.
  Orange is connected to GND.
  Green is connected to Vin.
