# Fritzing sketch id514_Scope2_0 (saved by Fritzing 0.8.3b)
circuit board: 6.88561cm x 5.36311cm
breadboards: 1

parts:
  R2 = Rotary Potentiometer (Small)
  R3 = Rotary Potentiometer (Small)
  R4 = Rotary Potentiometer (Small)
  U1 = BNC [package=bnc]
  Bauteil1 = Arduino Uno (Rev3)

nets:
  N1: R2.leg1, R3.leg1, R4.leg1, Bauteil1.5V
  N2: R2.wiper, Bauteil1.A2
  GND: R2.leg2, R3.leg2, R4.leg2, U1.GND, Bauteil1.GND
  N3: R3.wiper, Bauteil1.A3
  N4: R4.wiper, Bauteil1.A4/SDA
  N5: U1.OUT, Bauteil1.A1
