# Fritzing sketch id515_mpu6050_mega_0 (saved by Fritzing 0.7.12b)
breadboards: 1

parts:
  Arduino1 = Arduino Mega
  GY2 = MPU-6050 GY-521 [form="♀ (female)"]
  Part1 = FTDI Basic Programmer

nets:
  GND: Arduino1.GND, GY2.connector1, Part1.GND
  N1: Arduino1.D2, GY2.connector7
  N2: Arduino1.3V3, GY2.connector0
  N3: Arduino1.D16, Part1.RXI
  N4: Arduino1.D17, Part1.TXO
  N5: Arduino1.D20, GY2.connector3
  N6: Arduino1.D21, GY2.connector2
