# Fritzing sketch id516_Temp+Humidity_Display_0 (saved by Fritzing 0.9.3b)
circuit board: 8.46667cm x 5.64444cm
breadboards: 1

parts:
  Arduino_Mega_2560 = Arduino Mega 2560 (Rev3)
  R1 = Resistor [tolerance=±5% resistance=220 package=THT]
  LCD1 = LCD screen
  DHT22 = Humidity and Temperature Sensor RHT03
  R2 = Rotary Potentiometer (Small) [maximum_resistance=10kΩ package=THT]

nets:
  N1: Arduino_Mega_2560.D12_PWM, LCD1.RS
  N2: Arduino_Mega_2560.D11_PWM, LCD1.E
  5V: Arduino_Mega_2560.5V, R1.Pin_0, LCD1.VDD, LCD1.R/W, DHT22.Vcc, R2.leg1
  GND: Arduino_Mega_2560.GND, LCD1.VSS, LCD1.LED-, DHT22.GND_2, R2.leg2
  N3: Arduino_Mega_2560.D2_PWM, LCD1.DB7
  N4: Arduino_Mega_2560.D3_PWM, LCD1.DB6
  N5: Arduino_Mega_2560.D4_PWM, LCD1.DB5
  N6: Arduino_Mega_2560.D5_PWM, LCD1.DB4
  N7: Arduino_Mega_2560.D43, DHT22.Data-signal
  N8: R1.Pin_1, LCD1.LED+
