# Fritzing sketch id517_ARDUIN_SMD_1.4_0 (saved by Fritzing 0.9.2b)
circuit board: 5.42714cm x 10.2664cm
breadboards: 1

parts:
  R1 = Resistor [tolerance=±5% resistance=220 package="1206 [SMD]"]
  LED1 = smd LED [color="Red (633nm)" package="1206 [SMD]"]
  R2 = Resistor [tolerance=±5% resistance=220 package="1206 [SMD]"]
  LED2 = smd LED [color="Red (633nm)" package="1206 [SMD]"]
  R3 = Resistor [tolerance=±5% resistance=220 package="1206 [SMD]"]
  LED3 = smd LED [color="Red (633nm)" package="1206 [SMD]"]
  R4 = Resistor [tolerance=±5% resistance=220 package="1206 [SMD]"]
  LED4 = smd LED [color="Red (633nm)" package="1206 [SMD]"]
  R5 = Resistor [tolerance=±5% resistance=220 package="1206 [SMD]"]
  LED5 = smd LED [color="Red (633nm)" package="1206 [SMD]"]
  R6 = Resistor [tolerance=±5% resistance=220 package="1206 [SMD]"]
  LED6 = smd LED [color="Red (633nm)" package="1206 [SMD]"]
  R7 = Resistor [tolerance=±5% resistance=220 package="1206 [SMD]"]
  LED7 = smd LED [color="Red (633nm)" package="1206 [SMD]"]
  R8 = Resistor [tolerance=±5% resistance=220 package="1206 [SMD]"]
  LED8 = smd LED [color="Red (633nm)" package="1206 [SMD]"]
  R9 = Resistor [tolerance=±5% resistance=220 package="1206 [SMD]"]
  LED9 = smd LED [color="Red (633nm)" package="1206 [SMD]"]
  R10 = Resistor [tolerance=±5% resistance=220 package="1206 [SMD]"]
  LED10 = smd LED [color="Red (633nm)" package="1206 [SMD]"]
  R11 = Resistor [tolerance=±5% resistance=220 package="1206 [SMD]"]
  LED11 = smd LED [color="Red (633nm)" package="1206 [SMD]"]
  R12 = Resistor [tolerance=±5% resistance=220 package="1206 [SMD]"]
  LED12 = smd LED [color="Red (633nm)" package="1206 [SMD]"]
  IC1 = ULN2003A [package="SO16 [SMD]"]
  RGB_SMD_LED1 = SMD RGB LED (WS2812) [package=5050]
  RGB_SMD_LED2 = SMD RGB LED (WS2812) [package=5050]
  R13 = Resistor [tolerance=±5% resistance=220 package="1206 [SMD]"]
  R14 = Resistor [tolerance=±5% resistance=220 package="1206 [SMD]"]
  R15 = Resistor [tolerance=±5% resistance=220 package="1206 [SMD]"]
  R16 = Resistor [tolerance=±5% resistance=220 package="1206 [SMD]"]
  R17 = Resistor [tolerance=±5% resistance=220 package="1206 [SMD]"]
  R18 = Resistor [tolerance=±5% resistance=220 package="1206 [SMD]"]
  Súčiastka1 = Arduino Mega ADK (Rev3)
  JUMPER!!!!! = Resistor [tolerance=±5% resistance=0 package="1206 [SMD]"]
  R19 = Resistor [tolerance=±5% resistance=220 package="1206 [SMD]"]
  LED13 = smd LED [color="Red (633nm)" package="1206 [SMD]"]
  U1 = 74HC595 SMD [package="SO16 [SMD]"]
  JUMPER!!!!!_2 = Resistor [tolerance=±5% resistance=0 package="1206 [SMD]"]
  FOTOTRANZISTOR = smd LED [color="Red (633nm)" package="1206 [SMD]"]
  R20 = Resistor [tolerance=±5% resistance=1M package="1206 [SMD]"]
  RGB_SMD_LED3 = SMD RGB LED (WS2812) [package=5050]
  R21 = Resistor [tolerance=±5% resistance=220 package="1206 [SMD]"]
  U2 = V_REG_MC33269 [package=dpak]
  U3 = 3.5mm Audio Jack [package=audio-jack-3.5mm-smd]
  R22 = Trimmer Potentiometer [maximum_resistance=10kΩ package=THT]
  S1 = SWITCH-MOMENTARY-2 [package=tactile-switch-1101ne]
  C1 = Ceramic Capacitor [capacitance=100nF package="1206 [SMD, multilayer]"]
  C2 = Ceramic Capacitor [capacitance=100nF package="1206 [SMD, multilayer]"]
  SW1 = DIP SWITCH [package=dipswitch-02]
  SW2 = DIP Switch 8 Position [package=dipswitch-08]
  R23 = Resistor [tolerance=±5% resistance=1M package="1206 [SMD]"]
  R24 = Resistor [tolerance=±5% resistance=1M package="1206 [SMD]"]
  R25 = Resistor [tolerance=±5% resistance=1M package="1206 [SMD]"]
  R26 = Resistor [tolerance=±5% resistance=1M package="1206 [SMD]"]
  R27 = Resistor [tolerance=±5% resistance=1M package="1206 [SMD]"]
  R28 = Resistor [tolerance=±5% resistance=1M package="1206 [SMD]"]
  R29 = Resistor [tolerance=±5% resistance=1M package="1206 [SMD]"]
  R30 = Resistor [tolerance=±5% resistance=1M package="1206 [SMD]"]
  Pad1 = Pad [width=3.49386394461136 height=1.38287417225041 connect=center]
  Pad2 = Pad [width=3.49386394461136 height=1.38287417225041 connect=center]
  Pad3 = Pad [width=3.49386394461136 height=1.38287417225041 connect=center]
  Pad4 = Pad [width=3.49386394461136 height=1.38287417225041 connect=center]
  Pad5 = Pad [width=3.49386394461136 height=1.38287417225041 connect=center]
  Pad6 = Pad [width=3.49386394461136 height=1.38287417225041 connect=center]
  Pad7 = Pad [width=3.49386394461136 height=1.38287417225041 connect=center]
  Pad8 = Pad [width=3.49386394461136 height=1.38287417225041 connect=center]
  Pad9 = Pad [width=3.49386394461136 height=1.38287417225041 connect=center]
  Pad10 = Pad [width=3.49386394461136 height=1.38287417225041 connect=center]
  Pad11 = Pad [width=3.49386394461136 height=1.38287417225041 connect=center]
  Pad12 = Pad [width=3.49386394461136 height=1.38287417225041 connect=center]
  Pad13 = Pad [width=3.49386394461136 height=1.38287417225041 connect=center]
  Pad14 = Pad [width=3.49386394461136 height=1.38287417225041 connect=center]
  Pad15 = Pad [width=3.49386394461136 height=1.38287417225041 connect=center]
  Pad16 = Pad [width=3.49386394461136 height=1.38287417225041 connect=center]
  Pad17 = Pad [width=3.49386394461136 height=1.38287417225041 connect=center]
  Pad18 = Pad [width=3.49386394461136 height=1.38287417225041 connect=center]
  Pad19 = Pad [width=3.49386394461136 height=1.38287417225041 connect=center]
  Pad20 = Pad [width=3.49386394461136 height=1.38287417225041 connect=center]
  R31 = Resistor [tolerance=±5% resistance=1M package="1206 [SMD]"]
  R32 = Resistor [tolerance=±5% resistance=1M package="1206 [SMD]"]
  Pad22 = Pad [width=6.04701189595233 height=3.24438326119888 connect=center]
  Pad23 = Pad [width=3.46649322895601 height=3.68810746314568 connect=center]
  Pad24 = Pad [width=6.04701189595233 height=3.24438326119888 connect=center]
  R33 = Resistor [tolerance=±5% resistance=220 package="1206 [SMD]"]
  LED14 = smd LED [color="Red (633nm)" package="1206 [SMD]"]

nets:
  N1: R1.Pin_0, LED1.anode
  N2: R1.Pin_1, Súčiastka1.D13_PWM
  GND: LED1.cathode, LED2.cathode, LED3.cathode, LED4.cathode, LED5.cathode, LED6.cathode, LED7.cathode, LED8.cathode, LED9.cathode, LED10.cathode, LED11.cathode, LED12.cathode, IC1.0V, Súčiastka1.GND, U1.GND, JUMPER!!!!!_2.Pin_1, R20.Pin_0, R21.Pin_1, U2.GND, U3.LEFT, R22.leg2, S1.1, C1.0, C2.0, R23.Pin_1, R24.Pin_1, R25.Pin_1, R26.Pin_1, R27.Pin_0, R28.Pin_0, R29.Pin_0, R30.Pin_0, R31.Pin_1, R32.Pin_1, Pad24.pad, LED14.cathode
  N3: R2.Pin_0, LED2.anode
  N4: R2.Pin_1, Súčiastka1.D12_PWM
  N5: R3.Pin_0, LED3.anode
  N6: R3.Pin_1, Súčiastka1.D11_PWM
  N7: R4.Pin_0, LED4.anode
  N8: R4.Pin_1, Súčiastka1.D10_PWM
  N9: R5.Pin_0, LED5.anode
  N10: R5.Pin_1, Súčiastka1.D9_PWM
  N11: R6.Pin_0, LED6.anode
  N12: R6.Pin_1, Súčiastka1.D8_PWM
  N13: R7.Pin_0, LED7.anode
  N14: R7.Pin_1, Súčiastka1.D7_PWM
  N15: R8.Pin_0, LED8.anode
  N16: R8.Pin_1, Súčiastka1.D6_PWM
  N17: R9.Pin_0, LED9.anode
  N18: R9.Pin_1, Súčiastka1.D5_PWM
  N19: R10.Pin_0, LED10.anode
  N20: R10.Pin_1, Súčiastka1.D4_PWM
  N21: R11.Pin_0, LED11.anode
  N22: R11.Pin_1, Súčiastka1.D3_PWM
  N23: R12.Pin_0, LED12.anode
  N24: R12.Pin_1, Súčiastka1.D2_PWM
  N25: IC1.In_1, Súčiastka1.D34
  N26: IC1.In_2, Súčiastka1.D32
  N27: IC1.In_3, Súčiastka1.D30
  N28: IC1.In_4, Súčiastka1.D28
  N29: IC1.In_5, Súčiastka1.D26
  N30: IC1.In_6, Súčiastka1.D24
  N31: IC1.In_7, Súčiastka1.D22
  N32: IC1.COM_-_Common, R13.Pin_0, R14.Pin_0, R15.Pin_0, R16.Pin_0, R17.Pin_0, R18.Pin_0, JUMPER!!!!!.Pin_0, R19.Pin_0, U1.MR, U1.VCC, SW1.3, SW1.4, SW2.9, SW2.10, SW2.11, SW2.12, SW2.13, SW2.14, SW2.15, SW2.16, Pad1.pad, Pad2.pad, Pad3.pad, Pad4.pad, Pad5.pad, Pad6.pad, Pad7.pad, Pad8.pad, Pad9.pad, Pad10.pad
  N33: IC1.Out_7, RGB_SMD_LED1.VCC
  N34: IC1.Out_6, RGB_SMD_LED1.DIn
  N35: IC1.Out_5, RGB_SMD_LED1.DOut
  N36: IC1.Out_4, RGB_SMD_LED2.VCC
  N37: IC1.Out_3, RGB_SMD_LED2.DIn
  N38: IC1.Out_2, RGB_SMD_LED2.DOut
  N39: IC1.Out_1, LED13.anode
  N40: RGB_SMD_LED1.NC, R13.Pin_1
  N41: RGB_SMD_LED1.VDD, R14.Pin_1
  N42: RGB_SMD_LED1.VSS, R15.Pin_1
  N43: RGB_SMD_LED2.NC, R18.Pin_1
  N44: RGB_SMD_LED2.VDD, R17.Pin_1
  N45: RGB_SMD_LED2.VSS, R16.Pin_1
  N46: Súčiastka1.A8, SW1.1, Pad19.pad, R32.Pin_0
  N47: Súčiastka1.A9, SW1.2, Pad20.pad, R31.Pin_0
  N48: Súčiastka1.A10, R22.wiper, Pad23.pad
  N49: Súčiastka1.A15, FOTOTRANZISTOR.cathode, R20.Pin_1
  N50: Súčiastka1.A0, SW2.1, R27.Pin_1, Pad14.pad
  N51: Súčiastka1.A1, SW2.2, R28.Pin_1, Pad16.pad
  N52: Súčiastka1.A2, SW2.3, R30.Pin_1, Pad18.pad
  N53: Súčiastka1.A3, SW2.4, R29.Pin_1, Pad13.pad
  N54: Súčiastka1.A4, SW2.5, R26.Pin_0, Pad17.pad
  N55: Súčiastka1.A5, SW2.6, R25.Pin_0, Pad12.pad
  N56: Súčiastka1.A6, SW2.7, R24.Pin_0, Pad15.pad
  N57: Súčiastka1.A7, SW2.8, R23.Pin_0, Pad11.pad
  N58: Súčiastka1.RESET, S1.2
  N59: Súčiastka1.5V, JUMPER!!!!!.Pin_1, U2.OUT, C1.1, R33.Pin_0
  N60: Súčiastka1.D36, U1.DS
  N61: Súčiastka1.D38, U1.ST_CP
  N62: Súčiastka1.D40, U1.SH_CP
  N63: R19.Pin_1, LED13.cathode
  N64: U1.Q3, R22.leg1, Pad22.pad
  N65: U1.Q4, RGB_SMD_LED3.VSS
  N66: U1.Q5, RGB_SMD_LED3.VDD
  N67: U1.Q6, RGB_SMD_LED3.NC
  N68: U1.Q7, FOTOTRANZISTOR.anode
  N69: U1.OE, JUMPER!!!!!_2.Pin_0
  N70: RGB_SMD_LED3.DOut, RGB_SMD_LED3.DIn, RGB_SMD_LED3.VCC, R21.Pin_0
  N71: U2.IN, U3.RIGHT, U3.SLEEVE, C2.1
  N72: R33.Pin_1, LED14.anode

notes:
  1
  0
  3
  4
  5
  6
  2
  7
