# Fritzing sketch id518_arduino_mega_ISP_shield_0 (saved by Fritzing 0.9.0b)
perfboards: 1

parts:
  Деталь1 = Arduino Mega 2560 (Rev3)
  S1 = Toggle Switch [package=THT]
  C1 = Electrolytic Capacitor [capacitance=100µF package="200 mil [THT, electrolytic]"]

nets:
  N1: Деталь1.RESET, S1.COM
  N2: Деталь1.GND, S1.L1, C1.+
  N3: S1.L2, C1.-

notes:
  TX pin - goes to RX pin on AVR
  RX pin - goes to TX pin on AVR
  SCK
  MISO
  MOSI
  SS
  SO What should be done to TX/RX?
