# Fritzing sketch id519_Artduino_Mega_LCD_Shield_DIY_0 (saved by Fritzing 0.6.2b)
breadboards: 1

parts:
  S1 = Pushbutton [package="[THT]"]
  S2 = Pushbutton [package="[THT]"]
  S3 = Pushbutton [package="[THT]"]
  S4 = Pushbutton [package="[THT]"]
  Arduino_Mega_LCD_Shield = Arduino Mega
  R_1k = Resistor [tolerance=±5% resistance=1k package=THT]
  R_1k_2 = Resistor [tolerance=±5% resistance=1k package=THT]
  R_1k_3 = Resistor [tolerance=±5% resistance=1k package=THT]
  LCD = LCD screen
  potentiometer = Rotary Potentiometer (Small) [maximum_resistance=10kΩ]
  R_1k_4 = Resistor [tolerance=±5% resistance=1k package=THT]

nets:
  N1: S1.Pin_1, S1.Pin_2, Arduino_Mega_LCD_Shield.D37, R_1k_4.Pin_0
  +5V: S1.Pin_3, S1.Pin_4, S2.Pin_3, S2.Pin_4, S3.Pin_3, S3.Pin_4, S4.Pin_3, S4.Pin_4, Arduino_Mega_LCD_Shield.+5V, LCD.VDD, LCD.LED+, potentiometer.leg1
  N2: S2.Pin_1, S2.Pin_2, Arduino_Mega_LCD_Shield.D39, R_1k_2.Pin_0
  N3: S3.Pin_1, S3.Pin_2, Arduino_Mega_LCD_Shield.D43, R_1k_3.Pin_0
  N4: S4.Pin_1, S4.Pin_2, Arduino_Mega_LCD_Shield.D41, R_1k.Pin_0
  GND: Arduino_Mega_LCD_Shield.GND, R_1k.Pin_1, R_1k_2.Pin_1, R_1k_3.Pin_1, LCD.VSS, LCD.R/W, LCD.LED-, potentiometer.leg2, R_1k_4.Pin_1
  N5: Arduino_Mega_LCD_Shield.D38, LCD.DB7
  N6: Arduino_Mega_LCD_Shield.D40, LCD.DB6
  N7: Arduino_Mega_LCD_Shield.D42, LCD.DB5
  N8: Arduino_Mega_LCD_Shield.D44, LCD.DB4
  N9: Arduino_Mega_LCD_Shield.D46, LCD.E
  N10: Arduino_Mega_LCD_Shield.D48, LCD.RS
  N11: LCD.V0, potentiometer.wiper

notes:
  Arduino mega
  LCD Shield by effixe
  effixe@gmail.com
