# Fritzing sketch id51_2__button_0 (saved by Fritzing 0.9.3b)
breadboards: 1

parts:
  Part1 = Arduino Uno (Rev3) - ICSP
  S1 = Pushbutton [package="[THT]"]
  R1 = Resistor [tolerance=±5% resistance=220 package=THT]
  LED1 = LED - 5mm [color="Red (633nm)" package="5 mm [THT]"]

nets:
  N1: Part1.5V, S1.Pin_3, S1.Pin_4
  N2: Part1.D8, S1.Pin_1, S1.Pin_2, R1.Pin_0
  N3: Part1.GND, R1.Pin_1, LED1.cathode
  N4: Part1.AREF, LED1.anode
