# Fritzing sketch id520_lcd14x2wh1602a_0 (saved by Fritzing 0.7.12b)

parts:
  LCD1 = LCD screen
  U1 = Arduino Mega  # not connected
  R1 = Rotary Potentiometer (Small) [maximum_resistance=100kΩ]

nets:
  N1: LCD1.DB5, R1.wiper
  N2: LCD1.DB6, R1.leg1
