# Fritzing sketch id521_Arduino_mega_Joystick_Receiver_0 (saved by Fritzing 0.9.0b)

parts:
  NRF24L1 = NRF24L01
  Componente4 = Arduino Mega 2560 (Rev3)

nets:
  N1: NRF24L1.connector0, Componente4.3V3
  N2: NRF24L1.connector1, Componente4.D10_PWM
  N3: NRF24L1.connector2, Componente4.D51
  N4: NRF24L1.connector4, Componente4.GND
  N5: NRF24L1.connector5, Componente4.D9_PWM
  N6: NRF24L1.connector6, Componente4.D52
  N7: NRF24L1.connector7, Componente4.D50

notes:
  GND = Black
  VCC = Red
  CE = Yellow
  CSN = Green
  SCK = Orange
  MOSI = White
  MISO = Brown
  IRQ = Not Connected
  This connection are intended looking the TOP of the NRF24L01(as image suggested)
  if you "t u r n" the NRF24L01 upsidedown , take care to not invert some wire
  Arduino MEGA could be unstable on
  3.3 V output, so you have some problem , try to correct the ripple placing a 10uF capacitor.
  Usefull information on:
  http://arduino-info.wikispaces.com/Nrf24L01-2.4GHz-HowTo
