# Fritzing sketch id522_Arduino_menu_a_scelta_0 (saved by Fritzing 0.9.3b)
breadboards: 1

parts:
  LCD1 = LCD screen  # not connected
  Componente1 = Arduino Uno (Rev3)
  KY-1 = relè
  R1 = Resistor [tolerance=±5% resistance=220 package=THT]
  R2 = Resistor [tolerance=±5% resistance=220 package=THT]
  R3 = Resistor [tolerance=±5% resistance=10k package=THT]
  R4 = Resistor [tolerance=±5% resistance=10k package=THT]
  R5 = Resistor [tolerance=±5% resistance=10k package=THT]
  T1 = LM35 Temperature Sensor [package="TO92 [THT]"]
  LED1 = LED - 5mm [color="Red (633nm)" package="5 mm [THT]"]
  LED2 = LED - 5mm [color="Green (560nm)" package="5 mm [THT]"]
  SELEZIONA = Pushbutton [package="[THT]"]
  S2 = Pushbutton [package="[THT]"]
  S3 = Pushbutton [package="[THT]"]

nets:
  N1: Componente1.A0, T1.Vout
  N2: Componente1.D8, KY-1.connector0
  N3: Componente1.D10_PWM/SS, R3.Pin_0, SELEZIONA.Pin_1, SELEZIONA.Pin_2
  N4: Componente1.D11_PWM/MOSI, R5.Pin_0, S2.Pin_1, S2.Pin_2
  N5: Componente1.D12/MISO, R4.Pin_0, S3.Pin_1, S3.Pin_2
  N6: Componente1.D13/SCK, R1.Pin_1
  N7: Componente1.D1/TX, R2.Pin_1
  N8: Componente1.5V, KY-1.connector1, T1.+Vs, SELEZIONA.Pin_3, SELEZIONA.Pin_4, S2.Pin_3, S2.Pin_4, S3.Pin_3, S3.Pin_4
  GND: Componente1.GND, KY-1.connector2, R3.Pin_1, R4.Pin_1, R5.Pin_1, T1.GND, LED1.cathode, LED2.cathode
  N9: R1.Pin_0, LED1.anode
  N10: R2.Pin_0, LED2.anode

notes:
  TASTO
  SELEZIONA
  TASTI
  AVANTI - INDIETRO
  SENSORE TEMPERATURA LM35
  LAMPADINA
  230V
  SCL
  SDA
  DISPLAY LCD I2C
  PER MAGGIORI INFO:
  WWW.PROGETTIARDUINO.COM
