# Fritzing sketch id523_Arduino_meteo_nrf24l01_dht11_display_RX_0 (saved by Fritzing 0.9.2b)

parts:
  NRF24L1 = NRF24L01
  Arduino_Ricevitore_RX = Arduino Uno (Rev3)
  LCD1 = LCD screen  # not connected

nets:
  N1: NRF24L1.connector0, Arduino_Ricevitore_RX.3V3
  N2: NRF24L1.connector1, Arduino_Ricevitore_RX.D10_PWM/SS
  N3: NRF24L1.connector2, Arduino_Ricevitore_RX.D11_PWM/MOSI
  N4: NRF24L1.connector4, Arduino_Ricevitore_RX.GND
  N5: NRF24L1.connector5, Arduino_Ricevitore_RX.D9_PWM
  N6: NRF24L1.connector6, Arduino_Ricevitore_RX.D13/SCK
  N7: NRF24L1.connector7, Arduino_Ricevitore_RX.D12/MISO

notes:
  Collegamento display I2C
  Nero = GND
  Rosso = VCC
  Verde = SDA
  Blu= SCL
