# Fritzing sketch id524_Arduino_meteo_nrf24l01_dht11_display_TX_0 (saved by Fritzing 0.9.2b)
breadboards: 1

parts:
  DHT1 = dht11
  NRF24L1 = NRF24L01
  Arduino_Trasmettitore_TX = Arduino Uno (Rev3)
  R1 = Resistor [tolerance=±5% resistance=4.7k package=THT]

nets:
  N1: DHT1.connector1, Arduino_Trasmettitore_TX.5V, R1.Pin_0
  N2: DHT1.connector2, Arduino_Trasmettitore_TX.A0, R1.Pin_1
  N3: DHT1.connector4, NRF24L1.connector4, Arduino_Trasmettitore_TX.GND
  N4: NRF24L1.connector0, Arduino_Trasmettitore_TX.3V3
  N5: NRF24L1.connector1, Arduino_Trasmettitore_TX.D10_PWM/SS
  N6: NRF24L1.connector2, Arduino_Trasmettitore_TX.D11_PWM/MOSI
  N7: NRF24L1.connector5, Arduino_Trasmettitore_TX.D9_PWM
  N8: NRF24L1.connector6, Arduino_Trasmettitore_TX.D13/SCK
  N9: NRF24L1.connector7, Arduino_Trasmettitore_TX.D12/MISO
