# Fritzing sketch id525_metronome_0 (saved by Fritzing 0.9.2b)
breadboards: 1

parts:
  Part1 = Arduino Uno (Rev3)
  SP1 = SPEAKER [package=pcb_mount_speaker]
  LCD1 = LCD screen
  S1 = Pushbutton [package="[THT]"]
  LED1 = LEDs [package=led10mm]
  U1 = POT [package=trim_pot]
  R1 = Resistor [tolerance=±5% resistance=10k package=THT]
  R2 = Resistor [tolerance=±5% resistance=330 package="0805 [SMD]"]
  R3 = Resistor [tolerance=±5% resistance=330 package="0805 [SMD]"]

nets:
  N1: Part1.D8, SP1.-
  N2: Part1.D11_PWM/MOSI, LCD1.E
  N3: Part1.D12/MISO, LCD1.RS
  N4: Part1.D13/SCK, LED1.C
  GND: Part1.GND, SP1.+, LCD1.VSS, LCD1.LED-, U1.S, R3.Pin_0
  N5: Part1.D2, LCD1.DB7
  N6: Part1.D3_PWM, LCD1.DB6
  N7: Part1.D4, LCD1.DB5
  N8: Part1.D5_PWM, LCD1.DB4
  N9: Part1.D7, S1.Pin_1, S1.Pin_2, R1.Pin_1
  5V: Part1.5V, LCD1.VDD, LCD1.R/W, S1.Pin_3, S1.Pin_4, U1.A, R1.Pin_0, R2.Pin_0
  N10: LCD1.V0, U1.E
  N11: LCD1.LED+, R2.Pin_1
