# Fritzing sketch id526_micro_remote_0 (saved by Fritzing 0.8.5b)
circuit board: 8.46667cm x 5.64444cm
breadboards: 1

parts:
  Part1 = Arduino Micro (Rev3)  # not connected
  IR1 = TSOP312.., 314.. [package=THT]
  LED1 = LED - 5mm [color="Red (633nm)" package="5 mm [THT]"]
  R1 = Resistor [tolerance=±5% resistance=220 package=THT]
  R2 = Resistor [tolerance=±5% resistance=220 package=THT]

nets:
  N1: IR1.GND, LED1.cathode
  N2: IR1.Data, R2.Pin_1
  N3: LED1.anode, R1.Pin_1
