# Fritzing sketch id527_wirc_0 (saved by Fritzing 0.8.7b)
circuit board: 6.34479cm x 5.18137cm
breadboards: 1

parts:
  Micro = Arduino Nano (Rev3.0)
  Servo = female pin header, 4 pins [form="♀ (female)" part_number="RC out S"]
  J8 = female pin header, 4 pins [form="♀ (female)" part_number="RC out +"]
  J7 = female pin header, 4 pins [form="♀ (female)" part_number="RC out -"]
  J1 = female pin header, 4 pins [form="♀ (female)" part_number="prop Wi -"]
  RC_IN = female pin header, 4 pins [form="♀ (female)" part_number="RC in S"]
  J2 = female pin header, 4 pins [form="♀ (female)" part_number="prop Wi -"]
  Wi_IN_1-4 = female pin header, 4 pins [form="♀ (female)" part_number="prop Wi S"]
  I2C_Wi = female pin header, 4 pins [form="♀ (female)" part_number="I2C Wi"]
  J5 = female pin header, 4 pins [form="♀ (female)" part_number="RC in +"]
  J4 = female pin header, 4 pins [form="♀ (female)" part_number="RC in -"]
  RC/Bat = male pin header, 3 pins [form="♂ (male)" part_number="BAT or RC sel"]
  5V/VIN = male pin header, 3 pins [form="♂ (male)" part_number="PWR sel"]
  D1 = Rectifier Diode [part_number=1N4001 package="300 mil [THT]"]
  -SclSda+ = female pin header, 4 pins [form="♀ (female)" part_number="I2C out"]
  J16 = male pin header, 2 pins [form="♂ (male)" part_number="I2C sel1"]
  A4-5 = male pin header, 2 pins [form="♂ (male)" part_number="I2C sel2"]
  Wi_-+Bat = female pin header, 3 pins [form="♀ (female)" part_number="BAT Wi"]
  -+BatIN = male pin header, 3 pins [form="♂ (male)" part_number=BAT]
  OUT_Wi = female pin header, 4 pins [form="♀ (female)" part_number="Wi OUT"]
  J13 = male pin header, 4 pins [form="♂ (male)" part_number="Wi OUT sel1"]
  Wi_OUT = male pin header, 4 pins [form="♂ (male)" part_number="Wi OUT sel2"]
  IN_Wi = female pin header, 4 pins [form="♀ (female)" part_number="Wi IN"]
  J10 = male pin header, 4 pins [form="♂ (male)" part_number="Wi IN sel1"]
  Wi_IN = male pin header, 4 pins [form="♂ (male)" part_number="Wi IN sel2"]
  Spk&MicWi = female pin header, 4 pins [form="♀ (female)" part_number="AUDIO Wi"]
  Spk_&_Mic = male pin header, 4 pins [form="♂ (male)" part_number="AUDIO in/out"]
  R1 = Resistor [tolerance=±5% resistance=10k package=THT]
  R2 = Resistor [tolerance=±5% resistance=10k package=THT]

nets:
  N1: Micro.D1/TX, Wi_IN_1-4.pin3
  N2: Micro.D0/RX, Wi_IN_1-4.pin4
  N3: Micro.D2, Wi_IN_1-4.pin2
  N4: Micro.D3, Wi_IN_1-4.pin1
  N5: Micro.D4, RC_IN.pin4
  N6: Micro.D5, RC_IN.pin3
  N7: Micro.D6, RC_IN.pin2
  N8: Micro.D7, RC_IN.pin1
  N9: Micro.D8, Servo.pin4
  N10: Micro.D9, Servo.pin3
  N11: Micro.D10, Servo.pin2
  N12: Micro.D11/MOSI, Servo.pin1
  N13: Micro.D12/MISO, J13.pin3
  N14: Micro.VIN, 5V/VIN.pin3
  N15: Micro.5V, 5V/VIN.pin1
  N16: Micro.A7, J13.pin2
  N17: Micro.A6, J13.pin1
  N18: Micro.A5, J16.pin1
  N19: Micro.A4, J16.pin2
  N20: Micro.A3, J10.pin4
  N21: Micro.A2, J10.pin3
  N22: Micro.A1, J10.pin2
  N23: Micro.A0, J10.pin1
  N24: Micro.D13/SCK, J13.pin4
  N25: J8.pin1, J8.pin2, J8.pin3, J8.pin4, J2.pin1, J2.pin2, J2.pin3, J2.pin4, I2C_Wi.pin4, J5.pin1, J5.pin2, J5.pin3, J5.pin4, RC/Bat.pin1, -SclSda+.pin4, Wi_-+Bat.pin2, -+BatIN.pin2, R1.Pin_1, R2.Pin_1
  N26: J7.pin1, J7.pin2, J7.pin3, J7.pin4, J1.pin1, J1.pin2, J1.pin3, J1.pin4, I2C_Wi.pin1, J4.pin1, J4.pin2, J4.pin3, J4.pin4, -SclSda+.pin1, Wi_-+Bat.pin1, -+BatIN.pin1
  N27: I2C_Wi.pin2, -SclSda+.pin2, A4-5.pin1, R2.Pin_0
  N28: I2C_Wi.pin3, -SclSda+.pin3, A4-5.pin2, R1.Pin_0
  N29: RC/Bat.pin2, D1.anode
  N30: RC/Bat.pin3, Wi_-+Bat.pin3, -+BatIN.pin3
  N31: 5V/VIN.pin2, D1.cathode
  N32: OUT_Wi.pin1, Wi_OUT.pin1
  N33: OUT_Wi.pin2, Wi_OUT.pin2
  N34: OUT_Wi.pin3, Wi_OUT.pin3
  N35: OUT_Wi.pin4, Wi_OUT.pin4
  N36: IN_Wi.pin1, Wi_IN.pin1
  N37: IN_Wi.pin2, Wi_IN.pin2
  N38: IN_Wi.pin3, Wi_IN.pin3
  N39: IN_Wi.pin4, Wi_IN.pin4
  N40: Spk&MicWi.pin1, Spk_&_Mic.pin1
  N41: Spk&MicWi.pin2, Spk_&_Mic.pin2
  N42: Spk&MicWi.pin3, Spk_&_Mic.pin3
  N43: Spk&MicWi.pin4, Spk_&_Mic.pin4
