# Fritzing sketch id528_Modem_Arduino_0 (saved by Fritzing 0.8.5b)
circuit board: 6.88566cm x 5.36311cm
breadboards: 1

parts:
  R_DAC1 = Resistor [tolerance=±1% resistance=1k package=THT]
  R_DAC2 = Resistor [tolerance=±1% resistance=2.2k package=THT]
  R_DAC3 = Resistor [tolerance=±1% resistance=3.9k package=THT]
  R_DAC4 = Resistor [tolerance=±1% resistance=8.2k package=THT]
  Arduino = Arduino Uno (Rev3)
  C_DAC1 = Electrolytic Capacitor [capacitance=4.7µF voltage=50V package="100 mil [THT, electrolytic]"]
  C_DAC2 = Ceramic Capacitor [capacitance=100nF package="100 mil [THT, multilayer]"]
  R_DAC5 = Resistor [tolerance=±5% resistance=270 package=THT]
  MOD_OUT = female pin header, 1 pin [form="♀ (female)"]
  R_MODOUT_VDIV1 = Resistor [tolerance=±5% resistance=100k package=THT]
  R_MODOUT_VDIV2 = Resistor [tolerance=±5% resistance=1k package=THT]
  MOD_IN = female pin header, 1 pin [form="♀ (female)"]
  GND = female pin header, 1 pin [form="♀ (female)"]
  C_MODIN = Ceramic Capacitor [capacitance=1µF package="100 mil [THT, multilayer]"]
  R_MODIN_BIAS1 = Resistor [tolerance=±5% resistance=100k package=THT]
  R_MODIN_BIAS2 = Resistor [tolerance=±5% resistance=100k package=THT]
  N_MOSFET_PTT = MOSFET-NCHANNEL [part_number=2N7000 package=to-92]
  R_PTT_GATE = Resistor [tolerance=±5% resistance=10k package=THT]
  PTT_GND = female pin header, 1 pin [form="♀ (female)"]
  PTT_V+ = female pin header, 1 pin [form="♀ (female)"]
  LED_RX = LED - 3mm [color="Green (570nm)" package="3 mm [THT]"]
  LED_TX = LED - 3mm [color="Blue (505nm)" package="3 mm [THT]"]
  R_LED = Resistor [tolerance=±5% resistance=220 package=THT]

nets (from the pcb view):
  N1: R_DAC1.Pin_0, Arduino.D7
  N2: R_DAC1.Pin_1, R_DAC2.Pin_1, R_DAC3.Pin_1, R_DAC4.Pin_1, C_DAC1.-, C_DAC2.0, R_DAC5.Pin_0
  N3: R_DAC2.Pin_0, Arduino.D6_PWM
  N4: R_DAC3.Pin_0, Arduino.D5_PWM
  N5: R_DAC4.Pin_0, Arduino.D4
  N6: Arduino.A0, C_MODIN.0, R_MODIN_BIAS1.Pin_0, R_MODIN_BIAS2.Pin_0
  N7: Arduino.D9_PWM, LED_TX.anode
  N8: Arduino.D10_PWM/SS, LED_RX.anode
  N9: Arduino.GND, C_DAC2.1, R_DAC5.Pin_1, R_MODOUT_VDIV2.Pin_1, GND.pin1, R_MODIN_BIAS2.Pin_1, N_MOSFET_PTT.S, R_PTT_GATE.Pin_1, PTT_GND.pin1, R_LED.Pin_1
  N10: Arduino.D3_PWM, N_MOSFET_PTT.G, R_PTT_GATE.Pin_0
  N11: Arduino.5V, R_MODIN_BIAS1.Pin_1
  N12: C_DAC1.+, R_MODOUT_VDIV1.Pin_1
  N13: MOD_OUT.pin1, R_MODOUT_VDIV1.Pin_0, R_MODOUT_VDIV2.Pin_0
  N14: MOD_IN.pin1, C_MODIN.1
  N15: N_MOSFET_PTT.D, PTT_V+.pin1
  N16: LED_RX.cathode, LED_TX.cathode, R_LED.Pin_0

notes:
  RX/TX LEDs
  MOSFET for keying a radio's PTT
  +2.5v bias for ADC input
  4-bit resistor ladder DAC
  This voltage divider brings the output down to MIC level.
  On the Microduino version, there is also a tap on the PCB for line-level audio.
