# Fritzing sketch id52_2k_keypad_for_osu!_0 (saved by Fritzing 0.9.3b)

parts:
  S1 = Cherry MX Keyswitch
  S2 = Cherry MX Keyswitch
  R1 = Resistor [tolerance=±5% resistance=220 package=THT]
  R2 = Resistor [tolerance=±5% resistance=220 package=THT]
  Part1 = Arduino Micro (Rev3)
  RGB_SMD_LED1 = SMD RGB LED (WS2812) [package=5050]

nets:
  5V: S1.pin_1, S1.pin_9, S2.pin_1, S2.pin_10, Part1.5V, RGB_SMD_LED1.VCC
  N1: S1.pin_3, R2.Pin_0, Part1.D2/SDA
  N2: S2.pin_3, R1.Pin_0
  GND: R1.Pin_1, R2.Pin_1, Part1.GND, Part1.D5_PWM, RGB_SMD_LED1.VSS
  N3: Part1.D7, RGB_SMD_LED1.DIn
