# Fritzing sketch id530_Arduino_MIDI_Out__0 (saved by Fritzing 0.7.7b)
breadboards: 1

parts:
  Arduino1 = Arduino
  DIN1 = DIN-5 jack (MIDI) [package=THT]
  R3 = Resistor [resistance=220 tolerance=±5% package=THT]
  S1 = Pushbutton [package="[THT]"]
  R4 = Resistor [tolerance=±5% resistance=10k package=THT]

nets:
  N1: Arduino1.D7, S1.Pin_1, S1.Pin_2, R4.Pin_0
  N2: Arduino1.+5V, R3.Pin_0, S1.Pin_3, S1.Pin_4
  N3: Arduino1.GND, DIN1.2, R4.Pin_1
  N4: DIN1.4, R3.Pin_1
