# Fritzing sketch id531_lcdscreen_0 (saved by Fritzing 0.8.5b)
breadboards: 1

parts:
  Arduino1 = Arduino Mini (Rev5)
  VCC1 = Battery block 9V
  R1 = Rotary Potentiometer (Large) [maximum_resistance=100kΩ package=THT]
  LCD1 = LCD screen [part_number=QY-1602A]

nets:
  GND: Arduino1.GND, VCC1.-, R1.leg1, LCD1.VSS, LCD1.R/W, LCD1.LED-
  N1: Arduino1.D2, LCD1.DB7
  N2: Arduino1.D3_PWM, LCD1.DB6
  N3: Arduino1.D4, LCD1.DB5
  N4: Arduino1.D5_PWM, LCD1.DB4
  5V: Arduino1.5V, VCC1.+, R1.leg2, LCD1.VDD, LCD1.LED+
  N5: Arduino1.D12, LCD1.RS
  N6: Arduino1.D11_PWM, LCD1.E
  N7: R1.wiper, LCD1.V0
