# Fritzing sketch id532_schematic__0 (saved by Fritzing 0.9.2b)
circuit board: 8.46667cm x 5.64444cm
breadboards: 1

parts:
  Part1 = Arduino Uno (Rev3)
  R17 = Rotary Potentiometer (Small) [maximum_resistance=100kΩ package=THT]
  R18 = Rotary Potentiometer (Small) [maximum_resistance=100kΩ package=THT]
  R19 = Rotary Potentiometer (Small) [maximum_resistance=100kΩ package=THT]
  R20 = PHOTOCELL [package=photocell]
  R21 = PHOTOCELL [package=photocell]
  R22 = PHOTOCELL [package=photocell]
  S5 = Momentary Switch [package=ksa_sealed_tac_switch]
  S6 = Momentary Switch [package=ksa_sealed_tac_switch]
  S7 = Momentary Switch [package=ksa_sealed_tac_switch]
  S8 = Momentary Switch [package=ksa_sealed_tac_switch]
  R24 = Resistor [tolerance=±5% resistance=220 package="2512 [SMD]"]
  R25 = Resistor [tolerance=±5% resistance=220 package="2512 [SMD]"]
  R26 = Resistor [tolerance=±5% resistance=220 package="2512 [SMD]"]
  R30 = Resistor [tolerance=±5% resistance=220 package="2512 [SMD]"]
  R32 = Resistor [tolerance=±5% resistance=220 package="2512 [SMD]"]
  R33 = Resistor [tolerance=±5% resistance=220 package="2512 [SMD]"]
  R31 = Resistor [tolerance=±5% resistance=220 package="2512 [SMD]"]  # not connected

nets:
  N1: Part1.A0, R20.P$2, S5.1
  N2: Part1.A1, R21.P$2, R32.Pin_1
  N3: Part1.A2, R22.P$2, S6.1, R33.Pin_1
  N4: Part1.A3, R17.wiper
  N5: Part1.A4/SDA, R18.wiper
  N6: Part1.A5/SCL, R19.wiper
  N7: Part1.D9_PWM, S6.2, R26.Pin_0
  N8: Part1.D3_PWM, S5.2, R24.Pin_0
  N9: Part1.D5_PWM, S7.2, R30.Pin_0
  N10: Part1.D6_PWM, S8.2, R25.Pin_0
  N11: Part1.5V, R17.leg1, R18.leg1, R19.leg1, R20.P$1, R21.P$1, R22.P$1, S5.4, S6.4, S7.4, S8.1, S8.4
  N12: Part1.GND, R17.leg2, R18.leg2, R19.leg2, R24.Pin_1, R25.Pin_1, R26.Pin_1, R30.Pin_1, R32.Pin_0
