# Fritzing sketch id534_trinket_0 (saved by Fritzing 0.9.3b)
circuit board: 8.46667cm x 5.64444cm
breadboards: 1

parts:
  Part1 = Arduino Pro Mini v13
  Part2 = NRF24L01+ Breakout Board
  DS1 = DS18B20 1-Wire Temperature Sensor [part_number=DS18B20]
  R1 = Resistor [tolerance=±5% resistance=257 package=THT]

nets:
  GND: Part1.GND, Part2.GND, DS1.GND
  VCC: Part1.VCC, Part2.VCC, DS1.VDD, R1.Pin_1
  N1: Part1.D13/SCK, Part2.SCK
  N2: Part1.D12/MISO, Part2.MISO
  N3: Part1.D11_PWM/MOSI, Part2.MOSI
  N4: Part1.D10_PWM/SS, Part2.CS
  N5: Part1.D9_PWM, Part2.CE
  N6: Part1.D2, DS1.DQ, R1.Pin_0
