# Fritzing sketch id535_Arduino_mini_ver_05_Joystick_Receiver_0 (saved by Fritzing 0.9.0b)

parts:
  NRF24L1 = NRF24L01
  Arduino1 = Arduino Mini (Rev5)

nets:
  N1: NRF24L1.connector0, NRF24L1.connector4, Arduino1.GND
  N2: NRF24L1.connector1, Arduino1.D10_PWM
  N3: NRF24L1.connector2, Arduino1.D11_PWM
  N4: NRF24L1.connector5, Arduino1.D9_PWM
  N5: NRF24L1.connector6, Arduino1.D13
  N6: NRF24L1.connector7, Arduino1.D12

notes:
  GND = Black
  VCC = Red
  CE = Yellow
  CSN = Green
  SCK = Orange
  MOSI = White
  MISO = Brown
  IRQ = Not Connected
  This connection are intended looking the TOP of the NRF24L01(as image suggested)
  if you "t u r n" the NRF24L01 upsidedown , take care to not invert some wire
  NOTE:
  Stabilization circuit (3.3V) for NRF24L01 are suggested.
  But you can connect the VCC directly to +5 V .
