# Fritzing sketch id536_SteeringWheel.PNP.v2_0 (saved by Fritzing 0.9.2b)
circuit board: 6.63581cm x 2.50676cm
breadboards: 1

parts:
  Arduino_Nano = Arduino Nano (Rev3.0)
  100k = Resistor [tolerance=±5% resistance=220 package=THT]
  1k = Resistor [tolerance=±5% resistance=220 package=THT]
  2n3904 = TRANSISTOR_PNP [package=to-92]
  2n3906 = TRANSISTOR_PNP [package=to-92]
  J10 = female pin header, 4 pins [form="♀ (female)"]
  1k_2 = Resistor [tolerance=±5% resistance=220 package=THT]
  Sw_1_-_6 = screw terminal, 15 pins

nets:
  N1: Arduino_Nano.GND, 100k.Pin_1, 2n3904.E, J10.pin2, Sw_1_-_6.pin2, Sw_1_-_6.pin13, Sw_1_-_6.pin14
  N2: Arduino_Nano.D2, Sw_1_-_6.pin3
  N3: Arduino_Nano.D3, Sw_1_-_6.pin4
  N4: Arduino_Nano.D4, Sw_1_-_6.pin5
  N5: Arduino_Nano.D5, Sw_1_-_6.pin6
  N6: Arduino_Nano.D6, Sw_1_-_6.pin7
  N7: Arduino_Nano.D7, Sw_1_-_6.pin8
  N8: Arduino_Nano.D8, Sw_1_-_6.pin9
  N9: Arduino_Nano.D9, J10.pin4
  N10: Arduino_Nano.D10, J10.pin3
  N11: Arduino_Nano.D11/MOSI, Sw_1_-_6.pin10
  N12: Arduino_Nano.D12/MISO, Sw_1_-_6.pin12
  N13: Arduino_Nano.VIN, Sw_1_-_6.pin15
  N14: Arduino_Nano.5V, 2n3906.E, J10.pin1, Sw_1_-_6.pin11
  N15: Arduino_Nano.D13/SCK, 1k_2.Pin_0
  N16: 100k.Pin_0, 2n3904.B, 1k_2.Pin_1
  N17: 1k.Pin_0, 2n3906.B
  N18: 1k.Pin_1, 2n3904.C
  N19: 2n3906.C, Sw_1_-_6.pin1

notes:
  vcc
  gnd
  tx
  rx
  © russellweb.eu
  Bluetooth Module
  Neo
  5v
  12
  12v
  8
  7
  6
  5
  4
  3
  2
  Led
