# Fritzing sketch id537_Mosfet_Daughter_Board_0 (saved by Fritzing 0.9.1b)
circuit board: 4.72179cm x 3.19597cm
breadboards: 1

parts:
  Q7 = NPN-Transistor [package="TO92 [THT]"]
  Q8 = Basic FET P-Channel [package="TO220 [THT]"]
  R8 = Resistor [tolerance=±5% resistance=10k package=THT]
  R7 = Resistor [tolerance=±5% resistance=10k package=THT]
  Q9 = NPN-Transistor [package="TO92 [THT]"]
  Q10 = Basic FET P-Channel [package="TO220 [THT]"]
  R9 = Resistor [tolerance=±5% resistance=10k package=THT]
  R10 = Resistor [tolerance=±5% resistance=10k package=THT]
  Q11 = NPN-Transistor [package="TO92 [THT]"]
  R11 = Resistor [tolerance=±5% resistance=10k package=THT]
  R12 = Resistor [tolerance=±5% resistance=10k package=THT]
  Q13 = NPN-Transistor [package="TO92 [THT]"]
  Q14 = Basic FET P-Channel [package="TO220 [THT]"]
  R13 = Resistor [tolerance=±5% resistance=10k package=THT]
  R14 = Resistor [tolerance=±5% resistance=10k package=THT]
  Q12 = Basic FET P-Channel [package="TO220 [THT]"]
  J5 = screw terminal, 2 pins
  J6 = screw terminal, 2 pins
  J7 = screw terminal, 2 pins
  J8 = screw terminal, 2 pins
  J2 = screw terminal, 5 pins

nets:
  N1: Q7.E, Q9.E, Q11.E, Q13.E, J2.pin2
  N2: Q7.B, Q8.gate, R8.Pin_0
  N3: Q7.C, R7.Pin_0
  N4: Q8.drain, J5.pin1
  N5: Q8.source, R8.Pin_1, J5.pin2
  N6: R7.Pin_1, J2.pin5
  N7: Q9.B, Q10.gate, R10.Pin_0
  N8: Q9.C, R9.Pin_0
  N9: Q10.drain, J6.pin1
  N10: Q10.source, R10.Pin_1, J6.pin2
  N11: R9.Pin_1, J2.pin4
  N12: Q11.B, R12.Pin_0, Q12.gate
  N13: Q11.C, R11.Pin_0
  N14: R11.Pin_1, J2.pin3
  N15: R12.Pin_1, Q12.source, J7.pin2
  N16: Q13.B, Q14.gate, R14.Pin_0
  N17: Q13.C, R13.Pin_0
  N18: Q14.drain, J8.pin1
  N19: Q14.source, R14.Pin_1, J8.pin2
  N20: R13.Pin_1, J2.pin1
  N21: Q12.drain, J7.pin1

notes:
  Edge
  russellweb.eu
  Out | In 12v+
  1 - 2 - 3 - G - 4
