# Fritzing sketch id538_arduino_project_0 (saved by Fritzing 0.9.3b)
breadboards: 1

parts:
  S1 = Pushbutton [package=THT]
  S2 = Pushbutton [package=THT]
  S3 = Pushbutton [package=THT]
  S4 = Pushbutton [package=THT]
  S5 = Pushbutton [package=THT]
  J1 = Basic Force Sensing Resistor (FSR) [package=THT]
  Part1 = Arduino Pro Mini v13
  M1 = DC Motor
  M2 = DC Motor
  M3 = DC Motor
  Pololu_A1 = prefix0000
  Part2 = adafruit [part_number="Adafruit #3190"]

nets:
  N1: S1.leg0, Part1.D12/MISO
  N2: S1.leg1, S2.leg1, S3.leg1, S4.leg1, S5.leg1, J1.pin_0, Part1.VCC, Pololu_A1.connector1, Part2.connector7
  N3: S2.leg0, Part1.D13/SCK
  N4: S3.leg0, Part1.D11_PWM/MOSI
  N5: S4.leg0, Part1.D10_PWM/SS
  N6: S5.leg0, Part1.D9_PWM
  N7: J1.pin_1, Part1.D8
  N8: Part1.GND, Pololu_A1.connector0, Part2.connector6
  N9: Part1.D7, Pololu_A1.connector5
  N10: Part1.D6_PWM, Pololu_A1.connector4
  N11: Part1.D5_PWM, Pololu_A1.connector3
  N12: Part1.D4, Pololu_A1.connector2
  N13: Part1.D3_PWM, Part2.connector8
  N14: Part1.D2, Part2.connector9
  N15: M1.pin_1, Part2.connector27
  N16: M1.pin_2, Part2.connector28
  N17: M2.pin_1, Pololu_A1.connector13
  N18: M2.pin_2, Pololu_A1.connector12
  N19: M3.pin_1, Pololu_A1.connector11
  N20: M3.pin_2, Pololu_A1.connector10
