# Fritzing sketch id541_arduino_0 (saved by Fritzing 0.8.3b)
breadboards: 1

parts:
  IC1 = MICROCONTROLLER [package=dil28-3-simon-kit]
  S1 = Pushbutton [package="[THT]"]
  C1 = Electrolytic Capacitor [capacitance=10µF voltage=20V package="100 mil [THT, electrolytic]"]
  R1 = Resistor [tolerance=±5% resistance=10k package=THT]
  R2 = Resistor [tolerance=±5% resistance=220 package=THT]
  LED1 = LED - 5mm [color="Red (633nm)" package="5 mm [THT]"]
  C2 = Electrolytic Capacitor [capacitance=10µF voltage=20V package="100 mil [THT, electrolytic]"]
  U1 = Voltage Regulator [package=78xxl]
  VCC1 = Battery block 9V
  R3 = Resistor [tolerance=±5% resistance=220 package=THT]
  LED2 = LED - 5mm [color="Green (555nm)" package="5 mm [THT]"]
  Y1 = CRYSTAL [package=crystal-smd-10.5x4.8-2pin]

nets:
  N1: IC1.PC6(_RESET), S1.Pin_1, S1.Pin_2, R1.Pin_0
  N2: IC1.VCC, IC1.AVCC, IC1.AREF, C1.+, R1.Pin_1, R2.Pin_0, U1.OUT
  GND: IC1.GND, IC1.PB6(XTAL1_TOSC1), IC1.PB7(XTAL2_TOSC2), IC1.AGND, S1.Pin_3, S1.Pin_4, C1.-, LED1.cathode, C2.-, U1.GND, VCC1.-, R3.Pin_0, Y1.1, Y1.2
  N3: IC1.PB5(SCK), LED2.anode
  N4: R2.Pin_1, LED1.anode
  N5: C2.+, U1.IN, VCC1.+
  N6: R3.Pin_1, LED2.cathode

notes:
  ATENÇÃO: os componentes laranja e branco ligados aos pinos 9 e 10 do microcontrolador são os capacitores cerâmicos de 22pf e o com as perninhas azuis é o cristal de 16 MHz
