# Fritzing sketch id542_Fritzing_Wireing_for_Knight_Rider (saved by Fritzing 0.4.3b)
breadboards: 1

parts:
  Arduino1 = Arduino
  LED1 = Red LED - 5mm
  LED2 = Red LED - 5mm
  LED3 = Red LED - 5mm
  LED1_2 = Red LED - 5mm
  LED2_2 = Red LED - 5mm
  LED3_2 = Red LED - 5mm
  LED2_3 = Red LED - 5mm
  LED3_3 = Red LED - 5mm
  R1 = Rotary Potentiometer (Small)
  Power_plug1 = Power plug
  IC1 = ULN2803A [package=THT]

nets:
  N1: Arduino1.D12, IC1.In_1
  N2: Arduino1.D11, IC1.In_2
  N3: Arduino1.D10, IC1.In_3
  N4: Arduino1.D9, IC1.In_4
  N5: Arduino1.D6, IC1.In_5
  N6: Arduino1.D5, IC1.In_6
  N7: Arduino1.D3, IC1.In_7
  N8: Arduino1.D2, IC1.In_8
  N9: Arduino1.+5V, R1.leg2
  GND: Arduino1.GND, R1.leg1, Power_plug1.GND, IC1.0V
  N10: Arduino1.A0, R1.wiper
  N11: LED1.cathode, IC1.Out_8
  N12: LED1.anode, LED2.anode, LED3.anode, LED1_2.anode, LED2_2.anode, LED3_2.anode, LED2_3.anode, LED3_3.anode, Power_plug1.VCC
  N13: LED2.cathode, IC1.Out_7
  N14: LED3.cathode, IC1.Out_6
  N15: LED1_2.cathode, IC1.Out_5
  N16: LED2_2.cathode, IC1.Out_4
  N17: LED3_2.cathode, IC1.Out_3
  N18: LED2_3.cathode, IC1.Out_2
  N19: LED3_3.cathode, IC1.Out_1

notes:
  Pot to adjust speed
  We used Blue 12v mini LED
  modules from usLEDsupply.com
  12v DC from car battery or power supply
  (should be same
  voltage as your lights)
  in our case we just soldered onto the solder joints under the power jack on the bottom of the arduino so we only had one jack to mess with but you need to make sure your power source is within the rated range of your Arduino
