# Fritzing sketch id542_nano_v3_5110lcd_0 (saved by Fritzing 0.9.2b)
breadboards: 1

parts:
  Εξάρτημα1 = Arduino Nano (Rev3.0)
  Nokia_5110_LCD_Module1 = Nokia5110LCDModule

nets:
  N1: Εξάρτημα1.GND, Nokia_5110_LCD_Module1.connector1
  N2: Εξάρτημα1.D7, Nokia_5110_LCD_Module1.connector7
  N3: Εξάρτημα1.D8, Nokia_5110_LCD_Module1.connector6
  N4: Εξάρτημα1.D9, Nokia_5110_LCD_Module1.connector5
  N5: Εξάρτημα1.D10, Nokia_5110_LCD_Module1.connector4
  N6: Εξάρτημα1.D11/MOSI, Nokia_5110_LCD_Module1.connector3
  N7: Εξάρτημα1.D12/MISO, Nokia_5110_LCD_Module1.connector2
  N8: Εξάρτημα1.3V3, Nokia_5110_LCD_Module1.connector0
