# Fritzing sketch id543_devre_0 (saved by Fritzing 0.9.3b)
breadboards: 1

parts:
  L298N-Motor_Sürücü = Ponte-H L298N
  HC-05_Bluetooth_Modülü = Bluetooth HC-05 Macho  # not connected
  DC-Motor = DC Motor
  DC-Motor_2 = DC Motor
  Arduino_Nano = Arduino Nano (Rev3.0) (ICSP)
  PiL = BC9VPC [package=bc9vpc]

nets:
  N1: L298N-Motor_Sürücü.connector1, PiL.V+
  N2: L298N-Motor_Sürücü.connector2, Arduino_Nano.GND, PiL.V-
  N3: L298N-Motor_Sürücü.connector5, Arduino_Nano.D2
  N4: L298N-Motor_Sürücü.connector6, Arduino_Nano.D3
  N5: L298N-Motor_Sürücü.connector7, Arduino_Nano.D4
  N6: L298N-Motor_Sürücü.connector8, Arduino_Nano.D5
  N7: L298N-Motor_Sürücü.connector10, DC-Motor_2.pin_2
  N8: L298N-Motor_Sürücü.connector11, DC-Motor_2.pin_1
  N9: L298N-Motor_Sürücü.connector13, DC-Motor.pin_2
  N10: L298N-Motor_Sürücü.connector14, DC-Motor.pin_1

notes:
  BLUETTOH MODÜLÜ BAĞLANTISI (HC-05)
  -----------------------------------------------------------
  (Arduino Üzerinde) (Moto Sürücü Üzerinde)
  RX -------------------------------------> TX
  TX -------------------------------------> RX
  GND ---------------------------------> GND
  5V -----------------------------------> VCC
  -----------------------------------------------------------------------
  MOTOR SÜRÜCÜ BAĞLANTISI (L298N)
  (ARDUİNO-NANO) (MOTOR SÜRÜCÜ-L298N)
  D2 ----------------------------------------> İN1
  D3 ----------------------------------------> İN2
  D4 ----------------------------------------> İN3
  D5 ----------------------------------------> İN4
