# Fritzing sketch id544_nano_0 (saved by Fritzing 0.9.3b)
breadboards: 1

parts:
  Part1 = Arduino Nano (Rev3.0) (ICSP)
  Pololu_A1 = Pololu A4988 [package=SO16]
  Part2 = Bluetooth HC-05 Macho  # not connected
  J1 = Power Jack [package=power_jack_slot]
  M1 = Stepper Motor - Bipolar
  C1 = Capacitor Polarized [package=cpol-radial-10uf-25v]
  S1 = Toggle Switch [package=THT]
  S2 = Toggle Switch [package=THT]
  Q1 = TRANSISTOR_NPN [package=to-92]
  R1 = Resistor [tolerance=±5% resistance=220 package="1206 [SMD]"]

nets:
  GND: Part1.GND, Pololu_A1.GND, J1.GND, C1.-
  N1: Part1.D3, R1.Pin_1
  N2: Part1.D4, Pololu_A1.DIR
  N3: Part1.D6, Pololu_A1.STEP
  N4: Part1.D7, S2.COM
  N5: Part1.D8, S1.COM
  N6: Part1.VIN, J1.PWR
  5V: Part1.5V, Pololu_A1.VDD, Q1.C
  N7: Part1.3V3, Pololu_A1.MS2, S1.L1, S2.L1
  N8: Part1.D13/SCK, Pololu_A1.ENABLE
  N9: Pololu_A1.RESET, Pololu_A1.SLEEP
  N10: Pololu_A1.1B, M1.D
  N11: Pololu_A1.1A, M1.B
  N12: Pololu_A1.2A, M1.C
  N13: Pololu_A1.2B, M1.A
  N14: Pololu_A1.VMOT, C1.+
  N15: Q1.B, R1.Pin_0

notes:
  DC, 12v, 1A
