# Fritzing sketch id545_dht11_nano_v3_5110lcd_0 (saved by Fritzing 0.9.2b)
circuit board: 8.46667cm x 5.64444cm
breadboards: 1

parts:
  Εξάρτημα1 = Arduino Nano (Rev3.0)
  DHT2 = DHT11_Temperature_and_Humitidy_Sensor
  R3 = Resistor [tolerance=±5% resistance=10k package=THT]
  Nokia_5110_LCD_Module1 = Nokia5110LCDModule

nets:
  N1: Εξάρτημα1.GND, DHT2.connector4, Nokia_5110_LCD_Module1.connector1
  N2: Εξάρτημα1.D2, DHT2.connector2, R3.Pin_0
  N3: Εξάρτημα1.D7, Nokia_5110_LCD_Module1.connector7
  N4: Εξάρτημα1.D8, Nokia_5110_LCD_Module1.connector6
  N5: Εξάρτημα1.D9, Nokia_5110_LCD_Module1.connector5
  N6: Εξάρτημα1.D10, Nokia_5110_LCD_Module1.connector4
  N7: Εξάρτημα1.D11/MOSI, Nokia_5110_LCD_Module1.connector3
  N8: Εξάρτημα1.D12/MISO, Nokia_5110_LCD_Module1.connector2
  N9: Εξάρτημα1.5V, DHT2.connector1, R3.Pin_1
  N10: Εξάρτημα1.3V3, Nokia_5110_LCD_Module1.connector0
