# Fritzing sketch id546_akvaryum_sicaklik_0 (saved by Fritzing 0.9.3b)
breadboards: 1

parts:
  DHT1 = DHT11_Temperature_and_Humitidy_Sensor
  R1 = Resistor [tolerance=±5% resistance=10k package=THT]
  Parça1 = Arduino Nano (Rev3.0)
  LCD1 = LCD screen
  LCM1602_IIC1 = IC, DIP package, 22 pins [part_number="LCM1602 IIC" chip_label="LCM1602 IIC"]
  R2 = Temperature Sensor (Thermistor) [thermistor_type=NTC package=THT]
  R3 = Temperature Sensor (Thermistor) [thermistor_type=NTC package=THT]
  R4 = Temperature Sensor (Thermistor) [thermistor_type=NTC package=THT]
  R5 = Temperature Sensor (Thermistor) [thermistor_type=NTC package=THT]
  R6 = Resistor [tolerance=±5% resistance=10k package=THT]
  R7 = Resistor [tolerance=±5% resistance=10k package=THT]
  R8 = Resistor [tolerance=±5% resistance=10k package=THT]
  R9 = Resistor [tolerance=±5% resistance=10k package=THT]

nets:
  N1: DHT1.connector1, R1.Pin_0, Parça1.5V, LCM1602_IIC1.pin18, R2.pin_0, R3.pin_0, R4.pin_0, R5.pin_0
  N2: DHT1.connector2, R1.Pin_1, Parça1.D2
  N3: DHT1.connector4, Parça1.GND, LCM1602_IIC1.pin17, R6.Pin_0, R7.Pin_0, R8.Pin_0, R9.Pin_0
  N4: Parça1.A5, LCM1602_IIC1.pin20
  N5: Parça1.A4, LCM1602_IIC1.pin19
  N6: Parça1.A3, R2.pin_1, R6.Pin_1
  N7: Parça1.A2, R3.pin_1, R7.Pin_1
  N8: Parça1.A1, R4.pin_1, R8.Pin_1
  N9: Parça1.A0, R5.pin_1, R9.Pin_1
  N10: LCD1.VSS, LCM1602_IIC1.pin1
  N11: LCD1.VDD, LCM1602_IIC1.pin2
  N12: LCD1.V0, LCM1602_IIC1.pin3
  N13: LCD1.RS, LCM1602_IIC1.pin4
  N14: LCD1.R/W, LCM1602_IIC1.pin5
  N15: LCD1.E, LCM1602_IIC1.pin6
  N16: LCD1.DB0, LCM1602_IIC1.pin7
  N17: LCD1.DB1, LCM1602_IIC1.pin8
  N18: LCD1.DB2, LCM1602_IIC1.pin9
  N19: LCD1.DB3, LCM1602_IIC1.pin10
  N20: LCD1.DB4, LCM1602_IIC1.pin11
  N21: LCD1.DB5, LCM1602_IIC1.pin12
  N22: LCD1.DB6, LCM1602_IIC1.pin13
  N23: LCD1.DB7, LCM1602_IIC1.pin14
  N24: LCD1.LED+, LCM1602_IIC1.pin15
  N25: LCD1.LED-, LCM1602_IIC1.pin16
