# Fritzing sketch id547_Arduino_Nano_Dimmer_0 (saved by Fritzing 0.9.2b)
breadboards: 1

parts:
  IN = Screw terminal - 2 pins [package=THT]
  LAMP = Screw terminal - 2 pins [package=THT]
  IC1 = IC, DIP package, 6 pins [chip_label=4N25]
  R1 = Resistor [tolerance=±5% resistance=30k power=500mW package=THT]
  R2 = Resistor [tolerance=±5% resistance=30k power=500mW package=THT]
  Arduino_Nano = Arduino Nano (Rev3.0) (ICSP)
  R3 = Resistor [tolerance=±5% resistance=220 package="0805 [SMD]"]
  U1 = TRIAC [part_number=TIC206 package=to-92]
  IC2 = IC, DIP package, 6 pins [chip_label=MOC3041]
  R4 = Resistor [tolerance=±10% resistance=1k package="0805 [SMD]"]
  R5 = Resistor [tolerance=±5% resistance=220 package="0805 [SMD]"]
  LED1 = LED - 5mm [color="Red (633nm)" part_number=LED package="5 mm [THT]"]
  DI104 = IC, DIP package, 4 pins [chip_label=DI104]

nets:
  N1: IN.pin1, R1.Pin_1, U1.M2, R4.Pin_1
  N2: IN.pin2, LAMP.pin1, R2.Pin_1
  N3: LAMP.pin2, U1.M1
  N4: IC1.pin1, DI104.pin1
  N5: IC1.pin2, DI104.pin2
  N6: IC1.pin4, Arduino_Nano.GND
  N7: IC1.pin5, Arduino_Nano.D2, R3.Pin_1, IC2.pin2
  N8: R1.Pin_0, DI104.pin4
  N9: R2.Pin_0, DI104.pin3
  N10: Arduino_Nano.D3, R5.Pin_0
  N11: Arduino_Nano.5V, R3.Pin_0
  N12: U1.G, IC2.pin4
  N13: IC2.pin1, LED1.anode
  N14: IC2.pin6, R4.Pin_0
  N15: R5.Pin_1, LED1.cathode
