# Fritzing sketch id548_assignment_3_sketch_0 (saved by Fritzing 0.8.7b)
breadboards: 1

parts:
  Part1 = Arduino Nano (Rev3.0)
  R2 = Rotary Potentiometer (Small) [maximum_resistance=100kΩ package=THT]
  J2 = Basic Force Sensing Resistor (FSR) [package=THT]
  R6 = Rotary Potentiometer (Small) [maximum_resistance=100kΩ package=THT]
  R7 = Rotary Potentiometer (Small) [maximum_resistance=100kΩ package=THT]

nets:
  N1: Part1.GND, R2.leg1, R6.leg1, R7.leg1
  N2: Part1.5V, R2.leg2, J2.pin_0, R6.leg2, R7.leg2
  N3: Part1.A3, J2.pin_1
  N4: Part1.A2, R2.wiper
  N5: Part1.A1, R6.wiper
  N6: Part1.A0, R7.wiper
