# Fritzing sketch id549_ATTiny45_85_NanoISP_0 (saved by Fritzing 0.9.2b)
circuit board: 8.46667cm x 5.64444cm
breadboards: 1

parts:
  Bauteil2 = Arduino Nano (Rev3.0)
  LED1 = smd LED [color="Yellow (595nm)" package="0603 [SMD]"]
  R1 = Resistor [tolerance=±5% resistance=220 package="0402 [SMD]"]
  U1 = attiny85 [package=dip]

nets (from the breadboard view):
  N1: Bauteil2.D10, U1.Pin_1
  N2: Bauteil2.D11/MOSI, LED1.anode, U1.Pin_5
  N3: Bauteil2.D12/MISO, U1.Pin_6
  N4: Bauteil2.GND, R1.Pin_1, U1.Pin_4
  N5: Bauteil2.5V, U1.Pin_8
  N6: Bauteil2.D13/SCK, U1.Pin_7
  N7: LED1.cathode, R1.Pin_0
