# Fritzing sketch id54_Untitled_Sketch (saved by Fritzing 0.3.14b)
breadboards: 1

parts:
  VCC1 = obsolete Battery
  R5 = Resistor [resistance=220 package=THT]
  Q1 = NPN-Transistor [package="TO92 [THT]"]
  Q2 = NPN-Transistor [package="TO92 [THT]"]
  C3 = Ceramic Capacitor [package=THT]
  L1 = Inductor [package="400 mil [THT]"]
  R3 = Resistor [resistance=220 package=THT]
  C1 = Ceramic Capacitor [package=THT]
  R4 = Resistor [resistance=220 package=THT]
  C2 = Ceramic Capacitor [package=THT]
  R2 = Resistor [resistance=220 package=THT]
  R1 = Resistor [resistance=220 package=THT]
  C4 = Ceramic Capacitor [package=THT]
  ANT = Antenna
  Variable_Capacitor_C5 = Piezo Speaker
  MIC = Microphone
  C5 = Ceramic Capacitor [package=THT]

nets:
  N1: VCC1.-, R5.Pin_1, Q1.E, MIC.pin2, C5.pin_0
  N2: VCC1.+, L1.pin_1, C2.pin_1, R2.Pin_1, R1.Pin_0, Variable_Capacitor_C5.pin2, C5.pin_1
  N3: R5.Pin_0, Q2.E, C3.pin_0
  N4: Q1.B, R3.Pin_0, C1.pin_0
  N5: Q1.C, R3.Pin_1, R4.Pin_0
  N6: Q2.B, R4.Pin_1, C2.pin_0, R2.Pin_0
  N7: Q2.C, C3.pin_1, L1.pin_0, C4.pin_0, Variable_Capacitor_C5.pin1
  N8: C1.pin_1, R1.Pin_1, MIC.pin1
  N9: C4.pin_1, ANT.antenna_lead

notes:
  This is a high rang FM Transmitter designed by MARUF AHMAD
