# Fritzing sketch id550_4Pushs+LCD_Arduino_shield (saved by Fritzing 0.4.3b)
breadboards: 1

parts:
  S1 = Pushbutton [package="[THT]"]
  S2 = Pushbutton [package="[THT]"]
  S3 = Pushbutton [package="[THT]"]
  S4 = Pushbutton [package="[THT]"]
  R1 = Resistor [resistance=1k package=THT]
  R1_2 = Resistor [resistance=1k package=THT]
  R1_3 = Resistor [resistance=1k package=THT]
  R1_4 = Resistor [resistance=1k package=THT]
  LCD = LCD screen
  Arduino = Arduino

nets:
  N1: S1.Pin_1, S1.Pin_2, R1.Pin_0, Arduino.D10
  VDD: S1.Pin_3, S1.Pin_4, S2.Pin_3, S2.Pin_4, S3.Pin_3, S3.Pin_4, S4.Pin_3, S4.Pin_4, LCD.VDD, LCD.LED+, Arduino.+5V
  N2: S2.Pin_1, S2.Pin_2, R1_2.Pin_0, Arduino.D9
  N3: S3.Pin_1, S3.Pin_2, R1_3.Pin_0, Arduino.D12
  N4: S4.Pin_1, S4.Pin_2, R1_4.Pin_0, Arduino.D11
  VSS: R1.Pin_1, R1_2.Pin_1, R1_3.Pin_1, R1_4.Pin_1, LCD.VSS, LCD.V0, LCD.R/W, LCD.LED-, Arduino.GND
  N5: LCD.RS, Arduino.D8
  N6: LCD.E, Arduino.D7
  N7: LCD.DB4, Arduino.D6
  N8: LCD.DB5, Arduino.D5
  N9: LCD.DB6, Arduino.D4
  N10: LCD.DB7, Arduino.D3

notes:
  shield
