# Fritzing sketch id550_Nano_LCD1602A_0 (saved by Fritzing 0.9.3b)
breadboards: 1

parts:
  Bauteil1 = Arduino Nano (Rev3.0)
  R1 = Trimmer Potentiometer [maximum_resistance=10kΩ package=THT]
  U1 = LCD-16X2 [package=lcd-16x2]
  Bauteil2 = Arduino Mega 2560 (Rev3)

nets:
  GND: Bauteil1.GND, R1.leg2, U1.VSS, U1.R_W, U1.A, Bauteil2.GND
  N1: Bauteil1.D2, U1.DB7
  N2: Bauteil1.D3, U1.DB6
  N3: Bauteil1.D4, U1.DB5
  N4: Bauteil1.D5, U1.DB4
  N5: Bauteil1.D6, U1.E
  N6: Bauteil1.D7, U1.RS
  VIN: Bauteil1.VIN, R1.leg1, U1.VDD, U1.K, Bauteil2.5V
