# Fritzing sketch id552_Arduino_Nano_and_NRF24L01_+_LCD_I2C_YXrB3N7_0 (saved by Fritzing 0.9.3b)
breadboards: 1

parts:
  Part3 = Arduino Nano (Rev3.0)
  Part4 = NRF24L01+ Breakout Board
  LCM1602_IIC1 = generic_ic_dip_22_300mil.fzp [part_number="LCM1602 IIC" chip_label="LCM1602 IIC"]
  U1 = LCD-16X2 [package=lcd-16x2_noholes]

nets:
  GND: Part3.GND, Part4.GND, LCM1602_IIC1.connector16
  N1: Part3.D9, Part4.CE
  N2: Part3.D10, Part4.CS
  N3: Part3.D11/MOSI, Part4.MOSI
  N4: Part3.D12/MISO, Part4.MISO
  N5: Part3.5V, LCM1602_IIC1.connector17
  N6: Part3.A5, LCM1602_IIC1.connector19
  N7: Part3.A4, LCM1602_IIC1.connector18
  3V3: Part3.3V3, Part4.VCC
  N8: Part3.D13/SCK, Part4.SCK
  N9: LCM1602_IIC1.connector0, U1.VSS
  N10: LCM1602_IIC1.connector1, U1.VDD
  N11: LCM1602_IIC1.connector2, U1.VO
  N12: LCM1602_IIC1.connector3, U1.RS
  N13: LCM1602_IIC1.connector4, U1.R_W
  N14: LCM1602_IIC1.connector5, U1.E
  N15: LCM1602_IIC1.connector6, U1.DB0
  N16: LCM1602_IIC1.connector7, U1.DB1
  N17: LCM1602_IIC1.connector8, U1.DB2
  N18: LCM1602_IIC1.connector9, U1.DB3
  N19: LCM1602_IIC1.connector10, U1.DB4
  N20: LCM1602_IIC1.connector11, U1.DB5
  N21: LCM1602_IIC1.connector12, U1.DB6
  N22: LCM1602_IIC1.connector13, U1.DB7
  N23: LCM1602_IIC1.connector14, U1.A
  N24: LCM1602_IIC1.connector15, U1.K
