# Fritzing sketch id553_Arduino_nano_Joystick_Receiver_0 (saved by Fritzing 0.8.5b)
breadboards: 1

parts:
  NRF24L1 = NRF24L01
  Componente2 = Arduino Nano (Rev3.0) (ICSP)
  C1 = Electrolytic Capacitor [capacitance=10µF package="0405 [SMD, electrolytic]"]
  C2 = Tantalum Capacitor [capacitance=1pF voltage=0.1kV package="C 6032 [SMD, tantalum]"]
  C3 = Tantalum Capacitor [capacitance=100nF voltage=0.1kV package="C 6032 [SMD, tantalum]"]

nets:
  N1: NRF24L1.connector0, Componente2.3V3, C1.+, C2.+, C3.+
  N2: NRF24L1.connector1, Componente2.D10
  N3: NRF24L1.connector2, Componente2.D11/MOSI
  N4: NRF24L1.connector4, Componente2.GND, C1.-, C2.-, C3.-
  N5: NRF24L1.connector5, Componente2.D9
  N6: NRF24L1.connector6, Componente2.D13/SCK
  N7: NRF24L1.connector7, Componente2.D12/MISO

notes:
  GND = Black
  VCC = Red
  CE = Yellow
  CSN = Green
  SCK = Orange
  MOSI = White
  MISO = Brown
  IRQ = Not Connected
  This connection are intended looking the TOP of the NRF24L01(as image suggested)
  if you "t u r n" the NRF24L01 upsidedown , take care to not invert some wire
  10 uF
  Electrolytic
  1 pF
  Polyester
  100 nF
  Polyester
  Arduino Nano is extremely unstable on
  3.3 V output, so you need to correct the ripple placing some capacitors.
  With this configuration I've achieved the best results
