# Fritzing sketch id554_dht11_nano_v3_0 (saved by Fritzing 0.9.1b)
breadboards: 1

parts:
  Εξάρτημα1 = Arduino Nano (Rev3.0)
  DHT2 = DHT11_Temperature_and_Humitidy_Sensor
  R3 = Resistor [tolerance=±5% resistance=10k package=THT]

nets:
  N1: Εξάρτημα1.GND, DHT2.connector4, R3.Pin_1
  N2: Εξάρτημα1.D8, DHT2.connector2, R3.Pin_0
  N3: Εξάρτημα1.5V, DHT2.connector1
