# Fritzing sketch id555_Nano_LCD_1602_0 (saved by Fritzing 0.9.3b)
circuit board: 8.63248cm x 5.79433cm
breadboards: 1

parts:
  Arduino_Nano_V_3 = Arduino Nano (Rev3.0)
  LCD1 = LCD screen
  R1 = Trimmer Potentiometer [maximum_resistance=10kΩ package=THT]

nets:
  GND: Arduino_Nano_V_3.GND, LCD1.VSS, LCD1.R/W, LCD1.LED-, R1.leg1
  N1: Arduino_Nano_V_3.D2, LCD1.DB7
  N2: Arduino_Nano_V_3.D3, LCD1.DB6
  N3: Arduino_Nano_V_3.D4, LCD1.DB5
  N4: Arduino_Nano_V_3.D5, LCD1.DB4
  N5: Arduino_Nano_V_3.D11/MOSI, LCD1.E
  N6: Arduino_Nano_V_3.D12/MISO, LCD1.RS
  5V: Arduino_Nano_V_3.5V, LCD1.VDD, R1.leg2
  N7: Arduino_Nano_V_3.3V3, LCD1.LED+
  N8: LCD1.V0, R1.wiper
