# Fritzing sketch id557_ArduinoPacMan_0 (saved by Fritzing 0.9.1b)
breadboards: 1

parts:
  Part2 = 16x32_custom
  Part3 = Arduino Uno (Rev3) - ICSP
  BAT1 = BC9VPC [package=bc9vpc]  # not connected

nets:
  N1: Part2.connector128, Part3.D2
  N2: Part2.connector129, Part3.D3_PWM
  N3: Part2.connector130, Part3.D4
  N4: Part2.connector131, Part2.connector135, Part2.connector139, Part2.connector143, Part3.GND
  N5: Part2.connector132, Part3.D5_PWM
  N6: Part2.connector133, Part3.D6_PWM
  N7: Part2.connector134, Part3.D7
  N8: Part2.connector136, Part3.A0
  N9: Part2.connector137, Part3.A1
  N10: Part2.connector138, Part3.A2
  N11: Part2.connector140, Part3.D8
  N12: Part2.connector141, Part3.A3
  N13: Part2.connector142, Part3.D9_PWM
