# Fritzing sketch id558_arduino_pir_0 (saved by Fritzing 0.7.12b)
breadboards: 1

parts:
  Arduino1 = Arduino
  U1 = mystery part, 3 pins [chip_label="PIR Sensor"]

nets:
  N1: Arduino1.D12, U1.pin3
  N2: Arduino1.+5V, U1.pin2
  N3: Arduino1.GND, U1.pin1
