# Fritzing sketch id55_Two_motors_0 (saved by Fritzing 0.9.3b)
breadboards: 1

parts:
  R1 = Rotary Potentiometer (Small) [maximum_resistance=100kΩ package=THT]
  LCD1 = LCD screen
  Part1 = Arduino Uno (Rev3)
  M1 = DC Motor
  M2 = DC Motor
  IC1 = L293D [package=THT]
  VCC1 = Battery
  R3 = Rotary Potentiometer (Large) [maximum_resistance=100kΩ package=THT]  # not connected

nets:
  N1: R1.wiper, LCD1.V0
  VSS: R1.leg2, LCD1.VSS, LCD1.R/W, LCD1.LED-, Part1.GND, IC1.0V, VCC1.-
  VDD: LCD1.VDD, LCD1.LED+, Part1.5V, IC1.+Vmotor, IC1.+V, VCC1.+
  N2: LCD1.RS, Part1.D7
  N3: LCD1.E, Part1.D8
  N4: LCD1.DB4, Part1.D9_PWM
  N5: LCD1.DB5, Part1.D10_PWM/SS
  N6: LCD1.DB6, Part1.D11_PWM/MOSI
  N7: LCD1.DB7, Part1.D12/MISO
  N8: Part1.D3_PWM, IC1.In_2, IC1.In_3
  N9: Part1.D4, IC1.In_1, IC1.In_4
  N10: Part1.D5_PWM, IC1.Enable_1, IC1.Enable_2
  N11: M1.pin_1, IC1.Out_1_(_Controlled_by_Enable_1_)
  N12: M1.pin_2, IC1.Out_2_(_Controlled_by_Enable_1_)
  N13: M2.pin_1, IC1.Out_4_(_Controlled_by_Enable_2_)
  N14: M2.pin_2, IC1.Out_3_(_Controlled_by_Enable_2_)

notes:
  Speed control
  Motor direction
  LCD control
  Display control
