# Fritzing sketch id560_fritzing2_0 (saved by Fritzing 0.9.1b)
breadboards: 1

parts:
  Part2 = Arduino Uno (Rev3)
  R10 = Resistor [tolerance=±5% resistance=3.3k package=THT]
  R11 = Resistor [tolerance=±5% resistance=3.3k package=THT]
  R12 = Resistor [tolerance=±5% resistance=3.3k package=THT]
  R13 = TRIMPOT [package=trimpot_tc33]
  R14 = TRIMPOT [package=trimpot_tc33]
  R15 = TRIMPOT [package=trimpot_tc33]
  Q4 = LTR-301 [package=ltr-301]
  Q5 = LTR-301 [package=ltr-301]
  Q6 = LTR-301 [package=ltr-301]
  R16 = Resistor [package="2512 [SMD]"]
  R17 = Resistor [package="2512 [SMD]"]
  R18 = Resistor [package="2512 [SMD]"]
  LED4 = LED - 3mm [color="Red (633nm)" package="3 mm [THT]"]
  LED5 = LED - 3mm [color="Red (633nm)" package="3 mm [THT]"]
  LED6 = LED - 3mm [color="Red (633nm)" package="3 mm [THT]"]

nets:
  N1: Part2.D2, R10.Pin_1, Q4.C
  N2: Part2.D3_PWM, R12.Pin_1, Q5.C
  N3: Part2.D4, R11.Pin_1, Q6.C
  N4: Part2.5V, Q4.E, Q5.E, Q6.E, R16.Pin_0, R17.Pin_0, R18.Pin_0
  N5: Part2.GND, R13.CW, R14.CW, R15.CW
  N6: R10.Pin_0, R13.CCW, R13.WIPER
  N7: R11.Pin_0, R14.CCW, R14.WIPER
  N8: R12.Pin_0, R15.CCW, R15.WIPER
  N9: R16.Pin_1, LED6.anode
  N10: R17.Pin_1, LED5.anode
  N11: R18.Pin_1, LED4.anode
  N12: LED4.cathode, LED5.cathode, LED6.cathode

notes:
  3 Variable resistors (green)
