# Fritzing sketch id562_Arduino_cuisine___Module_de_puissance_RS232___20121120_0 (saved by Fritzing 0.7.10b)
breadboards: 1

parts:
  12V_R1 = Screw terminal - 2 pins [package=THT]
  G1_B1 = Screw terminal - 2 pins [package=THT]
  G2_B2 = Screw terminal - 2 pins [package=THT]
  12V_R2 = Screw terminal - 2 pins [package=THT]
  12V_R3 = Screw terminal - 2 pins [package=THT]
  12V_R4 = Screw terminal - 2 pins [package=THT]
  G3_B3 = Screw terminal - 2 pins [package=THT]
  G4_B4 = Screw terminal - 2 pins [package=THT]
  G6_B6 = Screw terminal - 2 pins [package=THT]
  G5_B5 = Screw terminal - 2 pins [package=THT]
  12V_R5 = Screw terminal - 2 pins [package=THT]
  12V_R6 = Screw terminal - 2 pins [package=THT]
  12V_R7 = Screw terminal - 2 pins [package=THT]
  12V_R8 = Screw terminal - 2 pins [package=THT]
  G7_B7 = Screw terminal - 2 pins [package=THT]
  G8_B8 = Screw terminal - 2 pins [package=THT]
  L6 = Screw terminal - 2 pins [package=THT]
  L5 = Screw terminal - 2 pins [package=THT]
  L4 = Screw terminal - 2 pins [package=THT]
  L3 = Screw terminal - 2 pins [package=THT]
  L2 = Screw terminal - 2 pins [package=THT]
  L1 = Screw terminal - 2 pins [package=THT]
  T01 = mystery part, 3 pins [chip_label=BD135 spacing=300mil part_number=BD135]
  T02 = mystery part, 3 pins [chip_label=BD135 spacing=300mil part_number=BD135]
  T03 = mystery part, 3 pins [chip_label=BD135 spacing=300mil part_number=BD135]
  T04 = mystery part, 3 pins [chip_label=BD135 spacing=300mil part_number=BD135]
  T05 = mystery part, 3 pins [chip_label=BD135 spacing=300mil part_number=BD135]
  T06 = mystery part, 3 pins [chip_label=BD135 spacing=300mil part_number=BD135]
  T07 = mystery part, 3 pins [chip_label=BD135 spacing=300mil part_number=BD135]
  T08 = mystery part, 3 pins [chip_label=BD135 spacing=300mil part_number=BD135]
  T09 = mystery part, 3 pins [chip_label=BD135 spacing=300mil part_number=BD135]
  T13 = mystery part, 3 pins [chip_label=BD135 spacing=300mil part_number=BD135]
  T11 = mystery part, 3 pins [chip_label=BD135 spacing=300mil part_number=BD135]
  T14 = mystery part, 3 pins [chip_label=BD135 spacing=300mil part_number=BD135]
  T12 = mystery part, 3 pins [chip_label=BD135 spacing=300mil part_number=BD135]
  T16 = mystery part, 3 pins [chip_label=BD135 spacing=300mil part_number=BD135]
  T15 = mystery part, 3 pins [chip_label=BD135 spacing=300mil part_number=BD135]
  T10 = mystery part, 3 pins [chip_label=BD135 spacing=300mil part_number=BD135]
  T19 = mystery part, 3 pins [chip_label=BD135 spacing=300mil part_number=BD135]
  T20 = mystery part, 3 pins [chip_label=BD135 spacing=300mil part_number=BD135]
  T22 = mystery part, 3 pins [chip_label=BD135 spacing=300mil part_number=BD135]
  T21 = mystery part, 3 pins [chip_label=BD135 spacing=300mil part_number=BD135]
  T24 = mystery part, 3 pins [chip_label=BD135 spacing=300mil part_number=BD135]
  T18 = mystery part, 3 pins [chip_label=BD135 spacing=300mil part_number=BD135]
  T17 = mystery part, 3 pins [chip_label=BD135 spacing=300mil part_number=BD135]
  T23 = mystery part, 3 pins [chip_label=BD135 spacing=300mil part_number=BD135]
  Res = IC, DIP package, 16 pins [chip_label="Resitor Array" spacing=300mil]
  ArduinoMega = Arduino Mega
  Res_2 = IC, DIP package, 16 pins [chip_label="Resitor Array" spacing=300mil]
  Res_3 = IC, DIP package, 16 pins [chip_label="Resitor Array" spacing=300mil]
  Res_4 = IC, DIP package, 16 pins [chip_label="Resitor Array" spacing=300mil]
  Temp = LM35 Temperature Sensor [part_number=T° package="TO92 [THT]"]
  TX1 = Screw terminal - 2 pins [package=THT]
  RX1 = Screw terminal - 2 pins [package=THT]
  T56 = mystery part, 3 pins [chip_label=BD135 spacing=300mil part_number=BD135]
  T55 = mystery part, 3 pins [chip_label=BD135 spacing=300mil part_number=BD135]
  T54 = mystery part, 3 pins [chip_label=BD135 spacing=300mil part_number=BD135]
  T53 = mystery part, 3 pins [chip_label=BD135 spacing=300mil part_number=BD135]
  T52 = mystery part, 3 pins [chip_label=BD135 spacing=300mil part_number=BD135]
  T51 = mystery part, 3 pins [chip_label=BD135 spacing=300mil part_number=BD135]
  R1 = Resistor [tolerance=±5% resistance=220 package=THT]
  R2 = Resistor [tolerance=±5% resistance=220 package=THT]
  Diag2 = LED - 5mm [color="Red (633nm)" package="5 mm [THT]"]
  Diag1 = LED - 5mm [color="Red (633nm)" package="5 mm [THT]"]
  Piezo_- = Piezo Speaker
  Piezo_+ = Piezo Speaker
  Serial = Screw terminal - 2 pins [package=THT]
  GND_+12V = Screw terminal - 2 pins [package=THT]
  +12V = Screw terminal - 2 pins [package=THT]
  Rel1&2/ = Screw terminal - 2 pins [package=THT]
  12V/GND/ = Screw terminal - 2 pins [package=THT]
  Term/+5V = Screw terminal - 2 pins [package=THT]
  T92 = mystery part, 3 pins [chip_label=BD135 spacing=300mil part_number=BD135]
  T91 = mystery part, 3 pins [chip_label=BD135 spacing=300mil part_number=BD135]
  C1 = Electrolytic Capacitor [capacitance=100µF voltage=16V package="100 mil [THT, electrolytic]"]
  Regul = Voltage Regulator - 5V [package="TO220 [THT]"]
  C3 = Electrolytic Capacitor [capacitance=100µF voltage=16V package="100 mil [THT, electrolytic]"]
  C4 = Electrolytic Capacitor [capacitance=100µF voltage=16V package="100 mil [THT, electrolytic]"]
  C5 = Ceramic Capacitor [capacitance=100nF package="100 mil [THT, multilayer]"]
  C6 = Ceramic Capacitor [capacitance=100nF package="100 mil [THT, multilayer]"]
  C2 = Electrolytic Capacitor [capacitance=100µF voltage=16V package="100 mil [THT, electrolytic]"]

nets:
  N1: 12V_R1.pin1, T01.pin2
  N2: 12V_R1.pin2, 12V_R2.pin2, 12V_R3.pin2, 12V_R4.pin2, 12V_R5.pin2, 12V_R6.pin2, 12V_R7.pin2, 12V_R8.pin2, L6.pin1, L5.pin1, L4.pin1, L3.pin1, L2.pin1, L1.pin1, GND_+12V.pin2, +12V.pin1, 12V/GND/.pin1, Regul.input_voltage, C4.+, C6.1, C2.+
  N3: G1_B1.pin1, T03.pin2
  N4: G1_B1.pin2, T02.pin2
  N5: G2_B2.pin1, T06.pin2
  N6: G2_B2.pin2, T05.pin2
  N7: 12V_R2.pin1, T04.pin2
  N8: 12V_R3.pin1, T07.pin2
  N9: 12V_R4.pin1, T10.pin2
  N10: G3_B3.pin1, T09.pin2
  N11: G3_B3.pin2, T08.pin2
  N12: G4_B4.pin1, T12.pin2
  N13: G4_B4.pin2, T11.pin2
  N14: G6_B6.pin1, T18.pin2
  N15: G6_B6.pin2, T17.pin2
  N16: G5_B5.pin1, T15.pin2
  N17: G5_B5.pin2, T14.pin2
  N18: 12V_R5.pin1, T13.pin2
  N19: 12V_R6.pin1, T16.pin2
  N20: 12V_R7.pin1, T19.pin2
  N21: 12V_R8.pin1, T22.pin2
  N22: G7_B7.pin1, T21.pin2
  N23: G7_B7.pin2, T20.pin2
  N24: G8_B8.pin1, T24.pin2
  N25: G8_B8.pin2, T23.pin2
  N26: L6.pin2, T51.pin2
  N27: L5.pin2, T52.pin2
  N28: L4.pin2, T53.pin2
  N29: L3.pin2, T54.pin2
  N30: L2.pin2, T55.pin2
  N31: L1.pin2, T56.pin2
  GND: T01.pin1, T02.pin1, T03.pin1, T04.pin1, T05.pin1, T06.pin1, T07.pin1, T08.pin1, T09.pin1, T13.pin1, T11.pin1, T14.pin1, T12.pin1, T16.pin1, T15.pin1, T10.pin1, T19.pin1, T20.pin1, T22.pin1, T21.pin1, T24.pin1, T18.pin1, T17.pin1, T23.pin1, ArduinoMega.GND, Temp.GND, TX1.pin1, RX1.pin2, T56.pin1, T55.pin1, T54.pin1, T53.pin1, T52.pin1, T51.pin1, Diag2.cathode, Diag1.cathode, Piezo_-.pin1, Piezo_-.pin2, GND_+12V.pin1, +12V.pin2, T92.pin1, T91.pin1, Regul.GND, C3.-, C4.-, C5.0, C6.0
  N32: T01.pin3, Res_3.pin15
  N33: T02.pin3, Res_3.pin16
  N34: T03.pin3, Res_3.pin14
  N35: T04.pin3, Res_3.pin13
  N36: T05.pin3, Res_3.pin12
  N37: T06.pin3, Res_3.pin11
  N38: T07.pin3, Res_3.pin10
  N39: T08.pin3, Res_3.pin9
  N40: T09.pin3, Res_2.pin16
  N41: T13.pin3, Res_2.pin12
  N42: T11.pin3, Res_2.pin14
  N43: T14.pin3, Res_2.pin11
  N44: T12.pin3, Res_2.pin13
  N45: T16.pin3, Res_2.pin9
  N46: T15.pin3, Res_2.pin10
  N47: T10.pin3, Res_2.pin15
  N48: T19.pin3, Res.pin14
  N49: T20.pin3, Res.pin13
  N50: T22.pin3, Res.pin11
  N51: T21.pin3, Res.pin12
  N52: T24.pin3, Res.pin10
  N53: T18.pin3, Res.pin15
  N54: T17.pin3, Res.pin16
  N55: T23.pin3, Res.pin9
  N56: Res.pin1, ArduinoMega.D14
  N57: Res.pin2, ArduinoMega.D15
  N58: Res.pin3, ArduinoMega.D16
  N59: Res.pin4, ArduinoMega.D17
  N60: Res.pin5, ArduinoMega.D2
  N61: Res.pin6, ArduinoMega.D3
  N62: Res.pin7, ArduinoMega.D20
  N63: Res.pin8, ArduinoMega.D21
  N64: ArduinoMega.D13, Res_3.pin7
  N65: ArduinoMega.D12, Res_3.pin8
  N66: ArduinoMega.D11, Res_2.pin1
  N67: ArduinoMega.D10, Res_2.pin2
  N68: ArduinoMega.D9, Res_2.pin3
  N69: ArduinoMega.D8, Res_2.pin4
  N70: ArduinoMega.D7, Res_2.pin5
  N71: ArduinoMega.D6, Res_2.pin6
  N72: ArduinoMega.D5, Res_2.pin7
  N73: ArduinoMega.D4, Res_2.pin8
  N74: ArduinoMega.D1TX, Serial.pin2
  N75: ArduinoMega.D0RX, Serial.pin1
  N76: ArduinoMega.+5V, Temp.+Vs, Term/+5V.pin2, C1.+, Regul.output_voltage, C3.+, C5.1
  N77: ArduinoMega.A0, Temp.Vout
  N78: ArduinoMega.D18, TX1.pin2
  N79: ArduinoMega.D19, RX1.pin1
  N80: ArduinoMega.D22, Res_3.pin6
  N81: ArduinoMega.D24, Res_3.pin5
  N82: ArduinoMega.D26, R1.Pin_1
  N83: ArduinoMega.D28, R2.Pin_1
  N84: ArduinoMega.D30, Res_3.pin4
  N85: ArduinoMega.D32, Res_3.pin3
  N86: ArduinoMega.D34, Res_3.pin2
  N87: ArduinoMega.D36, Res_3.pin1
  N88: ArduinoMega.D38, Res_4.pin8
  N89: ArduinoMega.D40, Res_4.pin7
  N90: ArduinoMega.D42, Res_4.pin6
  N91: ArduinoMega.D44, Res_4.pin5
  N92: ArduinoMega.D46, Res_4.pin4
  N93: ArduinoMega.D48, Res_4.pin3
  N94: ArduinoMega.D50, Res_4.pin2
  N95: ArduinoMega.D52, Res_4.pin1
  N96: ArduinoMega.D53, Piezo_+.pin1, Piezo_+.pin2
  N97: ArduinoMega.A10, Term/+5V.pin1
  N98: Res_4.pin9, T56.pin3
  N99: Res_4.pin10, T55.pin3
  N100: Res_4.pin11, T54.pin3
  N101: Res_4.pin12, T53.pin3
  N102: Res_4.pin13, T52.pin3
  N103: Res_4.pin14, T51.pin3
  N104: Res_4.pin15, T92.pin3
  N105: Res_4.pin16, T91.pin3
  N106: R1.Pin_0, Diag1.anode
  N107: R2.Pin_0, Diag2.anode
  N108: Rel1&2/.pin1, T91.pin2
  N109: Rel1&2/.pin2, T92.pin2
  N110: 12V/GND/.pin2, C1.-, C2.-

notes:
  MDL_Home
  November 2012
