# Fritzing sketch id563_Power_supply_0 (saved by Fritzing 0.8.3b)
circuit board: 5.3555cm x 2.05504cm
breadboards: 1

parts:
  J1 = Screw terminal - 2 pins [package=THT]
  R1 = Resistor [tolerance=±5% resistance=47 package=THT]
  D1 = Rectifier Diode [part_number=1N4007 package="300 mil [THT]"]
  D2 = Rectifier Diode [part_number=1N4007 package="300 mil [THT]"]
  D3 = Rectifier Diode [part_number=1N4007 package="300 mil [THT]"]
  D4 = Rectifier Diode [part_number=1N4007 package="300 mil [THT]"]
  U1 = Voltage Regulator - 5V [package="TO220 [THT]"]
  C2 = Ceramic Capacitor [capacitance=470µF voltage=35V package="100 mil [THT, multilayer]"]
  C3 = Electrolytic Capacitor [capacitance=10µF voltage=25V package="100 mil [THT, electrolytic]"]
  D5 = Zener Diode [part_number=1N4732A breakdown_voltage=3.6V package="300 mil [THT]"]
  C1 = Ceramic Capacitor [capacitance=4.7µF voltage=250V package="200 mil [THT, multilayer]"]
  R2 = Resistor [tolerance=±5% resistance=470 package=THT]

nets:
  N1: J1.pin1, D3.cathode, D4.anode
  N2: J1.pin2, R1.Pin_0
  N3: R1.Pin_1, C1.0, R2.Pin_0
  N4: D1.cathode, D4.cathode, U1.input_voltage, C2.1, D5.cathode
  N5: D1.anode, D2.cathode, C1.1, R2.Pin_1
  GND: D2.anode, D3.anode, U1.GND, C2.0, C3.-, D5.anode
  N6: U1.output_voltage, C3.+
