# Fritzing sketch id564_fritzing_sketch_0 (saved by Fritzing 0.6.3b)

parts:
  Arduino1 = Arduino
  J1 = Piezo Speaker
  J2 = Basic Servo
  R1 = Resistor [tolerance=±5% resistance=1k package=THT]

nets:
  GND: Arduino1.GND, J1.pin1, J2.gnd, R1.Pin_0
  N1: Arduino1.D7, J2.pulse
  N2: Arduino1.D5, Arduino1.RST
  3V3: Arduino1.3V3, J2.vcc
  N3: Arduino1.A1, J1.pin2, R1.Pin_1
