# Fritzing sketch id565_Blink72ISPv1_attiny (saved by Fritzing 0.6.4b)
breadboards: 1

parts:
  U1 = IC, DIP package, 8 pins [chip_label=ATTiny spacing=300mil]
  R1 = Resistor [tolerance=±0.25% resistance=100 package=THT]
  R2 = Resistor [tolerance=±0.25% resistance=100 package=THT]
  LED1 = RGB LED (6 legs) [package="5 mm [THT]"]
  LED2 = LED - 5mm [color="Red (660nm)" package="5 mm [THT]"]
  R3 = Photocell (LDR) [package=THT]
  R4 = Resistor [tolerance=±0.25% resistance=100 package=THT]
  T1 = LM34 Temperature Sensor [thermistor_type=PTC part_number="IR Receiver 38khz" package="TO92 [THT]"]
  VCC1 = Battery  # not connected

nets:
  N1: U1.pin2, R3.pin_0, R4.Pin_1
  N2: U1.pin3, T1.+Vs
  N3: U1.pin4, LED1.Green, LED2.cathode, R4.Pin_0, T1.Vout
  N4: U1.pin5, LED1.Blue1
  N5: U1.pin6, R1.Pin_1
  N6: U1.pin8, R2.Pin_1, R3.pin_1
  N7: R1.Pin_0, LED2.anode
  N8: R2.Pin_0, LED1.GND#1
