# Fritzing sketch id565_Power_Glove_Final_0 (saved by Fritzing 0.8.5b)
circuit board: 14cm x 7.00016cm
breadboards: 1

parts:
  ADXL1 = ADXL335_Accelerometer_Breakout
  R1 = Basic Flex Resistor
  R2 = Basic Flex Resistor
  R3 = Basic Flex Resistor
  R4 = Basic Flex Resistor
  R5 = Resistor [tolerance=±5% resistance=330 package=THT]
  R6 = Resistor [tolerance=±5% resistance=330 package=THT]
  R7 = Resistor [tolerance=±5% resistance=330 package=THT]
  R8 = Resistor [tolerance=±5% resistance=330 package=THT]
  S31 = pushbutton_2_horizontal.fzp
  S32 = pushbutton_2_horizontal.fzp
  S33 = pushbutton_2_horizontal.fzp
  S34 = pushbutton_2_horizontal.fzp
  S35 = pushbutton_2_horizontal.fzp
  S36 = pushbutton_2_horizontal.fzp
  S37 = pushbutton_2_horizontal.fzp
  S38 = pushbutton_2_horizontal.fzp
  S39 = pushbutton_2_horizontal.fzp
  S40 = pushbutton_2_horizontal.fzp
  S41 = pushbutton_2_horizontal.fzp
  S42 = pushbutton_2_horizontal.fzp
  S43 = pushbutton_2_horizontal.fzp
  S44 = pushbutton_2_horizontal.fzp
  S45 = pushbutton_2_horizontal.fzp
  S46 = pushbutton_2_horizontal.fzp
  S47 = pushbutton_2_horizontal.fzp
  S48 = pushbutton_2_horizontal.fzp
  S49 = pushbutton_2_horizontal.fzp
  S52 = pushbutton_2_horizontal.fzp
  S53 = pushbutton_2_horizontal.fzp
  S54 = pushbutton_2_horizontal.fzp
  S55 = pushbutton_2_horizontal.fzp
  S56 = pushbutton_2_horizontal.fzp
  S57 = pushbutton_2_horizontal.fzp
  LED2 = LED - 3mm [color="Red (633nm)" package="3 mm [THT]"]
  S58 = pushbutton_2_horizontal.fzp
  S59 = pushbutton_2_horizontal.fzp
  S60 = pushbutton_2_horizontal.fzp
  Pad1 = Pad [width=0.282222222222222 height=0.282222222222222 connect=center]
  Part3 = prefix0000 [form="♀ (female)"]
  Part4 = ArduinoBluetoothMatev13.fzp
  Pad2 = Pad [width=0.282222222222222 height=0.282222222222222 connect=center]
  Teensy_3_2 = Teensy 3.0

nets:
  N1: ADXL1.connector1, R1.Pin_2, R2.Pin_2, R3.Pin_2, R4.Pin_2, Part4.connector13, Teensy_3_2.3V3
  N2: ADXL1.connector3, R5.Pin_0, R6.Pin_0, R7.Pin_0, R8.Pin_0, S31.connector0, S32.connector0, S33.connector0, S34.connector0, S35.connector0, S36.connector0, S37.connector0, S38.connector0, S39.connector0, S40.connector0, S41.connector0, S42.connector1, S43.connector1, S44.connector1, S45.connector1, S46.connector1, S47.connector1, S48.connector1, S49.connector1, S52.connector0, S53.connector0, S54.connector0, S55.connector0, S56.connector0, S57.connector0, LED2.cathode, S58.connector1, S59.connector1, S60.connector0, Part3.connector1, Part4.connector14, Teensy_3_2.GND
  N3: ADXL1.connector4, Teensy_3_2.A5/D19
  N4: ADXL1.connector5, Teensy_3_2.A2/D16
  N5: ADXL1.connector6, Teensy_3_2.A0/D14
  N6: R1.pin_1, R5.Pin_1, Teensy_3_2.A12
  N7: R2.pin_1, R7.Pin_1, Teensy_3_2.A10
  N8: R3.pin_1, R6.Pin_1, Teensy_3_2.A13
  N9: R4.pin_1, R8.Pin_1, Teensy_3_2.A11
  N10: S31.connector1, Teensy_3_2.D33
  N11: S32.connector1, Teensy_3_2.A4/D18
  N12: S33.connector1, Teensy_3_2.A6/D20
  N13: S34.connector1, Teensy_3_2.D30
  N14: S35.connector1, S57.connector1, Teensy_3_2.A9/D23
  N15: S36.connector1, S41.connector1, Teensy_3_2.A8/D22
  N16: S37.connector1, Teensy_3_2.D32
  N17: S38.connector1, Teensy_3_2.A1/D15
  N18: S39.connector1, Teensy_3_2.A7/D21
  N19: S40.connector1, Teensy_3_2.A3/D17
  N20: S42.connector0, S43.connector0, Teensy_3_2.D6
  N21: S44.connector0, S45.connector0, Teensy_3_2.D5
  N22: S46.connector0, S47.connector0, Teensy_3_2.D4
  N23: S48.connector0, S49.connector0, Teensy_3_2.D3
  N24: S52.connector1, Teensy_3_2.D10
  N25: S53.connector1, Teensy_3_2.D11
  N26: S54.connector1, Teensy_3_2.D9
  N27: S55.connector1, Teensy_3_2.D12
  N28: S56.connector1, Pad1.pad, Teensy_3_2.D29
  N29: LED2.anode, Part4.connector16, Pad2.pad, Teensy_3_2.D8
  N30: S58.connector0, S59.connector0, Teensy_3_2.D2
  N31: S60.connector1, Teensy_3_2.D13
  N32: Part3.connector0, Teensy_3_2.Vin
  N33: Part4.connector15, Teensy_3_2.D7

notes:
  Computers Are Cool
