# Fritzing sketch id566_Arduino_blink_project_0 (saved by Fritzing 0.9.2b)
breadboards: 1

parts:
  Componente1 = Arduino Uno (Rev3)
  LED1 = smd LED [color="Orange (620nm)" package="0805 [SMD]"]
  R1 = Resistor [tolerance=±5% resistance=220 package="0805 [SMD]"]

nets:
  N1: Componente1.D13/SCK, R1.Pin_1
  N2: Componente1.GND, LED1.cathode
  N3: LED1.anode, R1.Pin_0
