# Fritzing sketch id567_Pro_Micro_USB_Serial_0 (saved by Fritzing 0.9.2b)
breadboards: 2

parts:
  Bauteil1 = Arduino Pro Mini v13
  J1 = shrouded pin header, 6 pins [form="♂ (shrouded male)"]  # not connected
  C1 = Ceramic Capacitor [capacitance=100nF package="100 mil [THT, multilayer]"]
  R1 = Resistor [tolerance=±5% resistance=1k package=THT]

nets:
  N1: Bauteil1.RESET, C1.0
  N2: C1.1, R1.Pin_0

notes:
  To Burn Firmware
  Usage as Usb-To-Serial (e.g. for Arduino IDE and Pro Mini)
