# Fritzing sketch id569_LGRemote (saved by Fritzing 0.9.3b)
circuit board: 7.99364cm x 7.46665cm

parts:
  part = smd LED [color="Red (633nm)" package="0805 [SMD]"]
  part_2 = smd LED [color="Red (633nm)" package="0805 [SMD]"]
  part_3 = Arduino Nano (Rev3.0)
  part_4 = LCD1602-I2C_
  part_5 = SWITCH_SPDT [package=kps-1290]
  part_6 = keypad4x3
  part_7 = Header 3 [package=molex-1x3_lock]

nets:
  N1: part.cathode, part_3.GND, part_4.connector0, part_5.O, part_7.2
  N2: part.anode, part_2.cathode
  N3: part_2.anode, part_3.D3
  N4: part_3.D2, part_5.P
  N5: part_3.D8, part_7.1
  N6: part_3.D12/MISO, part_4.connector1
  N7: part_3.A5, part_4.connector3
  N8: part_3.A4, part_4.connector2
  N9: part_3.A3, part_7.3
  N10: part_3.A1, part_6.connector25
  N11: part_3.3V3, part_6.connector27

notes:
  VCC
  GND
  Out
