# Fritzing sketch id569_Untitled_Sketch_0 (saved by Fritzing 0.9.3b)
circuit board: 1.94811cm x 3.42604cm
breadboards: 1

parts:
  IC1 = Voltage Regulator [package=78xxl]
  C1 = Ceramic Capacitor [capacitance=100nF package="100 mil [THT, multilayer]"]
  C2 = Ceramic Capacitor [capacitance=100nF package="100 mil [THT, multilayer]"]
  C3 = Electrolytic Capacitor [capacitance=1µF package="100 mil [THT, electrolytic]"]
  J1 = female pin header, 2 pins [form="♀ (female)"]
  J2 = female pin header, 12 pins [form="♀ (female)"]
  J3 = female pin header, 12 pins [form="♀ (female)"]

nets:
  GND: IC1.GND, C1.1, C2.0, C3.-, J1.pin2, J3.pin4
  N1: IC1.IN, C1.0, J1.pin1
  5V: IC1.OUT, C2.1, C3.+, J2.pin4
