# Fritzing sketch id570_arduino_programmer_0 (saved by Fritzing 0.9.3b)
breadboards: 1

parts:
  Onderdeel1 = Arduino Uno (Rev3)
  IC2 = Atmega8
  C1 = Electrolytic Capacitor [capacitance=10µF package="100 mil [THT, electrolytic]"]

nets:
  N1: Onderdeel1.D11_PWM/MOSI, IC2.connector15
  N2: Onderdeel1.D12/MISO, IC2.connector16
  N3: Onderdeel1.D13/SCK, IC2.connector17
  N4: Onderdeel1.5V, IC2.connector6, IC2.connector18, C1.-
  N5: Onderdeel1.GND, IC2.connector7, IC2.connector21, C1.+
