# Fritzing sketch id571_machine_0 (saved by Fritzing 0.9.2b)
breadboards: 1

parts:
  R1 = Resistor [tolerance=±5% resistance=220 package="2010 [SMD]"]
  R2 = Resistor [tolerance=±5% resistance=220 package="2010 [SMD]"]
  R3 = Resistor [tolerance=±5% resistance=220 package="2010 [SMD]"]
  LED1 = smd LED [color="Red (633nm)" package="0805 [SMD]"]
  LED2 = smd LED [color="Red (633nm)" package="0805 [SMD]"]
  LED3 = smd LED [color="Red (633nm)" package="0805 [SMD]"]
  Bauteil1 = Arduino Uno (Rev3) - ICSP
  R4 = Resistor [tolerance=±5% resistance=220 package=THT]
  S1 = SWITCH-MOMENTARY-2 [package=tactile_switch_tall]  # not connected

nets:
  N1: R1.Pin_0, Bauteil1.D6_PWM
  N2: R1.Pin_1, LED2.cathode
  N3: R2.Pin_0, Bauteil1.D7
  N4: R2.Pin_1, LED1.cathode
  N5: R3.Pin_0, Bauteil1.D5_PWM
  N6: R3.Pin_1, LED3.cathode
  N7: LED1.anode, LED2.anode, LED3.anode, Bauteil1.GND
  N8: Bauteil1.5V, R4.Pin_0
