# Fritzing sketch id572_Arduino_Bread_Board_0 (saved by Fritzing 0.9.3b)
circuit board: 8.46667cm x 5.64444cm
breadboards: 1

parts:
  Part2 = adafruit [part_number="Adafruit #1697"]
  R1 = Resistor [tolerance=±5% resistance=1k package="2512 [SMD]"]
  LED1 = smd LED [color="Red (633nm)" package="0603 [SMD]"]
  Part1 = Arduino Uno (Rev3) - ICSP

nets:
  N1: Part2.connector39, Part1.D13/SCK
  N2: Part2.connector40, Part1.D12/MISO
  N3: Part2.connector41, Part1.D11_PWM/MOSI
  N4: Part2.connector42, Part1.D10_PWM/SS
  N5: Part2.connector43, Part1.D2
  N6: Part2.connector45, Part1.D9_PWM
  N7: Part2.connector47, LED1.anode, Part1.GND
  N8: Part2.connector48, Part1.5V
  N9: R1.Pin_0, Part1.D3_PWM
  N10: R1.Pin_1, LED1.cathode
