# Fritzing sketch id577_Arduino_0 (saved by Fritzing 0.9.3b)
breadboards: 1

parts:
  C1 = Electrolytic Capacitor [capacitance=10μF package="0605 [SMD, electrolytic]"]
  U1 = Voltage Regulator - 5V [package="DPak [SMD]"]
  LED1 = LED - 5mm [color="Red (633nm)" package="5 mm [THT]"]
  R1 = Resistor [tolerance=±5% resistance=220 package=THT]
  C2 = Electrolytic Capacitor [capacitance=10μF package="0605 [SMD, electrolytic]"]
  LED2 = LED - 5mm [color="Red (633nm)" package="5 mm [THT]"]
  R2 = Resistor [tolerance=±5% resistance=220 package=THT]
  C3 = Ceramic Capacitor [capacitance=100nF package="100 mil [THT, multilayer]"]
  C4 = Ceramic Capacitor [capacitance=100nF package="100 mil [THT, multilayer]"]
  XTAL1 = Crystal [frequency="16 Mhz" package=THT]
  Part1 = FTDI Basic Programmer
  U2 = atmega328 [package=dip]
  S1 = Pushbutton [package="[THT]"]

nets:
  GND: C1.-, U1.GND, R1.Pin_0, C2.-, R2.Pin_1, C3.0, C4.1, Part1.GND, U2.RESET, U2.GND, S1.Pin_1, S1.Pin_2, S1.Pin_3, S1.Pin_4
  N1: C1.+, U1.input_voltage
  N2: U1.output_voltage, LED1.anode, C2.+, Part1.POWER, U2.VCC, U2.AVCC
  N3: LED1.cathode, R1.Pin_1
  N4: LED2.cathode, R2.Pin_0
  N5: LED2.anode, U2.D13
  N6: C3.1, XTAL1.pin_1, U2.XLAT1
  N7: C4.0, XTAL1.pin_0, U2.XLAT2
  N8: Part1.RXI, U2.D1_(TX)
  N9: Part1.TXO, U2.D0_(RX)
