# Fritzing sketch id579_Arduino_PWM_Breakout_0 (saved by Fritzing 0.7.5b)
breadboards: 1

parts:
  Arduino1 = Arduino
  J1 = male pin header, 3 pins [form="♂ (male)"]
  J2 = male pin header, 3 pins [form="♂ (male)"]
  J3 = male pin header, 3 pins [form="♂ (male)"]
  J4 = male pin header, 3 pins [form="♂ (male)"]
  J5 = male pin header, 3 pins [form="♂ (male)"]
  J6 = male pin header, 3 pins [form="♂ (male)"]

nets:
  N1: Arduino1.D11, J1.pin3
  N2: Arduino1.D10, J2.pin3
  N3: Arduino1.D9, J3.pin3
  N4: Arduino1.D6, J4.pin3
  N5: Arduino1.D5, J5.pin3
  N6: Arduino1.D3, J6.pin3
  N7: J1.pin1, J2.pin1, J3.pin1, J4.pin1, J5.pin1, J6.pin1
  N8: J1.pin2, J2.pin2, J3.pin2, J5.pin2, J6.pin2
