# Fritzing sketch id580_arduino_pwm_led_control_0 (saved by Fritzing 0.9.3b)

parts:
  Part2 = Arduino Uno (Rev3)
  U1 = ENCODER-QUADRATURE [package=encoder-16mm-quad]
  Q1 = Basic FET N-Channel [part_number=IRF540 package="D2Pak [SMD]"]
  Q2 = NPN-Transistor [package="TO92 [THT]"]
  Q3 = PNP-Transistor [package="TO92 [THT]"]
  R1 = Resistor [tolerance=±5% resistance=1k package="2512 [SMD]"]
  R2 = Resistor [tolerance=±5% resistance=1k package="2512 [SMD]"]
  D1 = LTE-302 [part_number="10W 12v" package=lte-302]
  D2 = LTE-302 [part_number="10W 12v" package=lte-302]
  D3 = LTE-302 [part_number="10W 12v" package=lte-302]
  D4 = LTE-302 [part_number="10W 12v" package=lte-302]
  D5 = LTE-302 [part_number="10W 12v" package=lte-302]
  D6 = LTE-302 [part_number="10W 12v" package=lte-302]
  R3 = Resistor [tolerance=±5% resistance=10k package="2512 [SMD]"]
  R4 = Resistor [tolerance=±5% resistance=10k package="2512 [SMD]"]
  S1 = SWITCH-MOMENTARY-2 [package=tactile_switch_smd-2]
  Power_plug1 = Power plug [part_number=12V-20V]
  LM1 = RioRand LM2596

nets:
  N1: Part2.D8, U1.B, R3.Pin_0
  N2: Part2.D11_PWM/MOSI, R2.Pin_0
  N3: Part2.D12/MISO, U1.A, R4.Pin_0
  N4: Part2.GND, U1.C, Q1.source, Q3.C, S1.2, LM1.Pin_3
  N5: Part2.D4, S1.1
  N6: Part2.5V, Q2.C, R3.Pin_1, R4.Pin_1
  N7: Part2.VIN, D1.A, D2.A, D3.A, D4.A, D5.A, D6.A, LM1.Pin_2
  N8: Q1.Gate, R1.Pin_1
  N9: Q1.drain, D1.C, D2.C, D3.C, D4.C, D5.C, D6.C
  N10: Q2.E, Q3.E, R1.Pin_0
  N11: Q2.B, Q3.B, R2.Pin_1
  N12: Power_plug1.VCC, LM1.Pin_0
  N13: Power_plug1.GND, LM1.Pin_1
