# Fritzing sketch id581_marnieros2_0 (saved by Fritzing 0.8.5b)
circuit board: 9.42002cm x 7.02979cm
breadboards: 2

parts:
  LM324 = IC, DIP package, 14 pins [chip_label=IC]
  R2 = Resistor [tolerance=±5% resistance=22k package=THT]
  R3 = Resistor [tolerance=±5% resistance=22k package=THT]
  R4 = Resistor [tolerance=±5% resistance=22k package=THT]
  R5 = Resistor [tolerance=±5% resistance=22k package=THT]
  R6 = Resistor [tolerance=±5% resistance=22k package=THT]
  R7 = Resistor [tolerance=±5% resistance=22k package=THT]
  R8 = Resistor [tolerance=±5% resistance=22k package=THT]
  R9 = Resistor [tolerance=±5% resistance=22k package=THT]
  R11 = Resistor [tolerance=±5% resistance=22k package=THT]
  R12 = Resistor [tolerance=±5% resistance=22k package=THT]
  R13 = Resistor [tolerance=±5% resistance=22k package=THT]
  R14 = Resistor [tolerance=±5% resistance=22k package=THT]
  C3 = Electrolytic Capacitor [capacitance=10µF voltage=35V package="100 mil [THT, electrolytic]"]
  C4 = Electrolytic Capacitor [capacitance=10µF voltage=35V package="100 mil [THT, electrolytic]"]
  C2 = Electrolytic Capacitor [capacitance=10µF voltage=35V package="100 mil [THT, electrolytic]"]
  C1 = Electrolytic Capacitor [capacitance=10µF voltage=35V package="100 mil [THT, electrolytic]"]
  PWM = screw terminal, 4 pins
  GND = Screw terminal - 2 pins [package=THT]
  Pad1 = Pad [width=6.73995030048465 height=7.2791774457241 connect=center]
  J6 = Power Jack [package=power_jack_slot]
  OUT = screw terminal, 4 pins

nets:
  N1: LM324.pin1, R7.Pin_0, OUT.pin4
  N2: LM324.pin2, R6.Pin_1, R7.Pin_1
  N3: LM324.pin3, R5.Pin_0, C2.+
  N4: LM324.pin4, J6.PWR
  N5: LM324.pin5, R9.Pin_1, C4.+
  N6: LM324.pin6, R8.Pin_0, R11.Pin_1
  N7: LM324.pin7, R8.Pin_1, OUT.pin3
  N8: LM324.pin8, R14.Pin_1, OUT.pin1
  N9: LM324.pin9, R4.Pin_0, R14.Pin_0
  N10: LM324.pin10, R2.Pin_1, C1.+
  N11: LM324.pin11, R4.Pin_1, R6.Pin_0, R11.Pin_0, R12.Pin_1, C3.-, C4.-, C2.-, C1.-, GND.pin1, GND.pin2, Pad1.pad, J6.GND
  N12: LM324.pin12, R3.Pin_0, C3.+
  N13: LM324.pin13, R12.Pin_0, R13.Pin_1
  N14: LM324.pin14, R13.Pin_0, OUT.pin2
  N15: R2.Pin_0, PWM.pin1
  N16: R3.Pin_1, PWM.pin2
  N17: R5.Pin_1, PWM.pin4
  N18: R9.Pin_0, PWM.pin3
