# Fritzing sketch id583_Arduino_RC_Car___Connessione_0 (saved by Fritzing 0.7.1b)
breadboards: 1

parts:
  Motore_per_Sterzata_a_destra_e_a_sinistra = DC Motor
  Motore_per_Accellerazione_e_Retromarcia = DC Motor
  Arduino1 = Arduino
  Integrato_L293D = L293D [package=THT]
  Pacco_Batteria_9_Volt_-_o_12_Volt_-_in_base_ai_motori = Battery
  Power_plug1 = Power plug  # not connected
  Alimentazione_Arduino = Battery block 9V  # not connected

nets:
  N1: Motore_per_Sterzata_a_destra_e_a_sinistra.pin_1, Integrato_L293D.Out_2_(_Controlled_by_Enable_1_)
  N2: Motore_per_Sterzata_a_destra_e_a_sinistra.pin_2, Integrato_L293D.Out_1_(_Controlled_by_Enable_1_)
  N3: Motore_per_Accellerazione_e_Retromarcia.pin_1, Integrato_L293D.Out_4_(_Controlled_by_Enable_2_)
  N4: Motore_per_Accellerazione_e_Retromarcia.pin_2, Integrato_L293D.Out_3_(_Controlled_by_Enable_2_)
  N5: Arduino1.D7, Integrato_L293D.In_2
  N6: Arduino1.D6, Integrato_L293D.In_1
  N7: Arduino1.D4, Integrato_L293D.In_3
  N8: Arduino1.D3, Integrato_L293D.In_4
  N9: Arduino1.+5V, Integrato_L293D.Enable_1, Integrato_L293D.Enable_2
  N10: Arduino1.GND, Integrato_L293D.0V, Pacco_Batteria_9_Volt_-_o_12_Volt_-_in_base_ai_motori.-
  N11: Integrato_L293D.+Vmotor, Integrato_L293D.+V, Pacco_Batteria_9_Volt_-_o_12_Volt_-_in_base_ai_motori.+
