# Fritzing sketch id586_Remote_Presenter_0 (saved by Fritzing 0.9.3b)
circuit board: 4.58345cm x 4.76025cm
breadboards: 1

parts:
  RX = RF-LINK_RX [package=rf-link_rx]
  Arduino_32u4_Beetle = Arduino Pro Mini v13
  ANT = Antenna

nets:
  GND: RX.GND, Arduino_32u4_Beetle.GND
  N1: RX.DATA, Arduino_32u4_Beetle.D1/RX
  +5V: RX.+5V, Arduino_32u4_Beetle.VCC
  N2: RX.ANT, ANT.antenna_lead
