# Fritzing sketch id587_ArduinoRemplaceBouton_(1)_0 (saved by Fritzing 0.8.7b)
breadboards: 1

parts:
  Q2 = NPN-Transistor [package="TO92 [THT]"]
  Composant1 = Arduino Uno (Rev3)
  R2 = Resistor [tolerance=±5% resistance=1k package=THT]
  LED1 = LED - 5mm [color="Green (570nm)" package="5 mm [THT]"]
  R3 = Resistor [tolerance=±5% resistance=1k package=THT]
  LED2 = LED - 5mm [color="Red (633nm)" package="5 mm [THT]"]

nets:
  N1: Q2.E, Composant1.GND, LED2.cathode
  N2: Q2.B, R2.Pin_1
  N3: Q2.C, R3.Pin_0
  N4: Composant1.D13/SCK, LED2.anode
  N5: Composant1.D4, R2.Pin_0
  N6: Composant1.3V3, LED1.cathode
  N7: LED1.anode, R3.Pin_1
