# Fritzing sketch id588_RGB_Led_0 (saved by Fritzing 0.9.2b)

parts:
  Eleman1 = Arduino Nano (Rev3.0)
  LED1 = RGB LED (com. cathode, rbg) [package="5 mm [THT]"]

nets:
  N1: Eleman1.GND, LED1.common_cathode
  N2: Eleman1.D9, LED1.red_anode
  N3: Eleman1.D10, LED1.green_anode
  N4: Eleman1.D11/MOSI, LED1.blue_anode
