# Fritzing sketch id589_LED_BIT_BT_LAMP_1_0 (saved by Fritzing 0.9.3b)
perfboards: 2

parts:
  LED1 = LED - 5mm [color="Red (660nm)" package="5 mm [THT]"]
  LED2 = LED - 5mm [color="Red (660nm)" package="5 mm [THT]"]
  LED3 = LED - 5mm [color="Green (570nm)" package="5 mm [THT]"]
  LED4 = LED - 5mm [color="Green (570nm)" package="5 mm [THT]"]
  LED5 = LED - 5mm [color="Blue (525nm)" package="5 mm [THT]"]
  LED6 = LED - 5mm [color="Blue (525nm)" package="5 mm [THT]"]
  LED7 = LED - 5mm [color="White (6500K)" package="5 mm [THT]"]
  LED8 = LED - 5mm [color="White (6500K)" package="5 mm [THT]"]
  R1 = Resistor [tolerance=±5% resistance=220 package=THT]
  R2 = Resistor [tolerance=±5% resistance=220 package=THT]
  R4 = Resistor [tolerance=±5% resistance=220 package=THT]
  R5 = Resistor [tolerance=±5% resistance=220 package=THT]
  R6 = Resistor [tolerance=±5% resistance=220 package=THT]
  R7 = Resistor [tolerance=±5% resistance=220 package=THT]
  R8 = Resistor [tolerance=±5% resistance=220 package=THT]
  R9 = Resistor [tolerance=±5% resistance=220 package=THT]
  Bauteil1 = Arduino Nano (Rev3.0)
  Bauteil2 = Bluetooth HC-05 Macho
  R10 = Resistor [tolerance=±5% resistance=2.2k package=THT]
  R11 = Resistor [tolerance=±5% resistance=2k package=THT]
  Power_plug1 = Power plug
  S1 = Toggle Switch [package=THT]
  S2 = Toggle Switch [package=THT]

nets:
  N1: LED1.cathode, LED2.cathode, Bauteil1.D3
  N2: LED1.anode, R9.Pin_0
  N3: LED2.anode, R2.Pin_0
  N4: LED3.cathode, LED4.cathode, Bauteil1.D5
  N5: LED3.anode, R4.Pin_0
  N6: LED4.anode, R8.Pin_0
  N7: LED5.cathode, LED6.cathode, Bauteil1.D6
  N8: LED5.anode, R5.Pin_0
  N9: LED6.anode, R7.Pin_0
  N10: LED7.cathode, LED8.cathode, Bauteil1.D9
  N11: LED7.anode, R6.Pin_1
  N12: LED8.anode, R1.Pin_0
  GND: R1.Pin_1, R2.Pin_1, R4.Pin_1, R5.Pin_1, R6.Pin_0, R7.Pin_1, R8.Pin_1, R9.Pin_1, Bauteil1.GND, Power_plug1.GND
  N13: Bauteil1.D1/TX, S2.L1
  N14: Bauteil1.D0/RX, S1.L1
  VIN: Bauteil1.VIN, Power_plug1.VCC
  3V3: Bauteil1.3V3, Bauteil2.VCC
  N15: Bauteil2.TXD, S1.COM
  N16: Bauteil2.RXD, R11.Pin_1
  N17: Bauteil2.GND, R10.Pin_0
  N18: R11.Pin_0, S2.COM, S2.L2

notes:
  5V 1A
  RGB COMMEN GND
