# Fritzing sketch id591_LED_BIT_BT_LAMP_1_common_+_RGB_Stripe_0 (saved by Fritzing 0.9.3b)
perfboards: 1

parts:
  Bauteil1 = Arduino Nano (Rev3.0)
  Bauteil2 = Bluetooth HC-05 Macho
  R10 = Resistor [tolerance=±20% resistance=2k package=THT]
  R11 = Resistor [tolerance=±20% resistance=1k package=THT]
  Power_plug1 = Power plug
  S1 = Toggle Switch [package=THT]
  S2 = Toggle Switch [package=THT]
  LED1 = Super Flux RGB LED (com. anode)
  LED2 = Super Flux RGB LED (com. anode)
  LED3 = Super Flux RGB LED (com. anode)
  LED4 = Super Flux RGB LED (com. anode)
  Q1 = NPN-Transistor [package="TO92 [THT]"]
  Q2 = NPN-Transistor [package="TO92 [THT]"]
  Q3 = NPN-Transistor [package="TO92 [THT]"]

nets:
  N1: Bauteil1.D1/TX, S2.L1
  N2: Bauteil1.D0/RX, S1.L1
  GND: Bauteil1.GND, Power_plug1.GND, Q2.C
  N3: Bauteil1.D3, Q2.B
  N4: Bauteil1.D5, Q1.B
  N5: Bauteil1.D6, Q3.B
  VIN: Bauteil1.VIN, Power_plug1.VCC, LED1.common_anode, LED2.common_anode, LED3.common_anode, LED4.common_anode
  5V: Bauteil1.5V, Bauteil2.VCC
  N6: Bauteil2.TXD, S1.COM
  N7: Bauteil2.RXD, R10.Pin_1, R11.Pin_1
  N8: Bauteil2.GND, R10.Pin_0
  N9: R11.Pin_0, S2.COM, S2.L2
  N10: LED1.red_cathode, LED2.red_cathode, LED3.red_cathode, LED4.red_cathode, Q2.E
  N11: LED1.blue_cathode, LED2.blue_cathode, LED3.blue_cathode, LED4.blue_cathode, Q3.E
  N12: LED1.green_cathode, LED2.green_cathode, LED3.green_cathode, LED4.green_cathode, Q1.E

notes:
  12V 1A
  Common Annode C+
