# Fritzing sketch id593_Arduino_robot_con_telecomando_e_controllo_IR_0 (saved by Fritzing 0.9.2b)
breadboards: 1

parts:
  Componente1 = Arduino Uno (Rev3)
  BAT1 = BC9VPC [package=bc9vpc]
  M1 = DC Motor
  M2 = DC Motor
  Q1 = NPN-Transistor [package="TO92 [THT]"]
  Q2 = NPN-Transistor [package="TO92 [THT]"]
  IR = TSOP312.., 314.. [part_number=1838B package=THT]

nets:
  N1: Componente1.D8, Q2.B
  N2: Componente1.D9_PWM, Q1.B
  N3: Componente1.GND, BAT1.V-, Q1.E, Q2.E, IR.Vs
  N4: Componente1.D1/TX, IR.GND
  N5: Componente1.5V, M1.pin_2, M2.pin_1, IR.Data
  N6: Componente1.VIN, BAT1.V+
  N7: M1.pin_1, Q2.C
  N8: M2.pin_2, Q1.C
