# Fritzing sketch id594_arm_0 (saved by Fritzing 0.9.3b)
breadboards: 1

parts:
  Part1 = Arduino Uno (Rev3)
  J1 = Basic Servo
  J2 = Basic Servo
  J3 = Basic Servo

nets:
  N1: Part1.D3_PWM, J1.pulse
  N2: Part1.D5_PWM, J2.pulse
  N3: Part1.D6_PWM, J3.pulse
  VCC: Part1.5V, J1.vcc, J2.vcc, J3.vcc
  GND: Part1.GND, J1.gnd, J2.gnd, J3.gnd
