# Fritzing sketch id595_senseboard_0 (saved by Fritzing 0.7.11b)
breadboards: 1

parts:
  R1 = Photocell (LDR) [package=THT]
  T1 = LM35 Temperature Sensor [package="TO92 [THT]"]
  Arduino1 = Arduino
  R2 = Resistor [tolerance=±5% resistance=1k package=THT]

nets:
  N1: R1.pin_0, Arduino1.A2, R2.Pin_1
  GND: R1.pin_1, T1.GND, Arduino1.GND
  N2: T1.+Vs, Arduino1.+5V, R2.Pin_0
  N3: T1.Vout, Arduino1.A1
