# Fritzing sketch id59_2__octaves_0 (saved by Fritzing 0.9.3b)
circuit board: 21.9237cm x 16.1415cm
circuit board: 9.74323cm x 10.906cm
circuit board: 8.78334cm x 11.0912cm
breadboards: 1

parts:
  pot1 = Resistor [tolerance=±5% resistance=220 package=THT]
  C1 = Ceramic Capacitor [capacitance=100nF package="100 mil [THT, multilayer]"]
  VCC1 = Battery
  audio_out = Audio Jack (TRS) 3.5mm [package="PG203J [THT]"]
  IC1 = IC, DIP package, 14 pins [chip_label=IC]
  pot2 = Resistor [tolerance=±5% resistance=220 package=THT]
  C2 = Ceramic Capacitor [capacitance=100nF package="100 mil [THT, multilayer]"]
  HEF1 = HEF4094 [package="DIP16 [THT]"]
  HEF2 = HEF4094 [package="DIP16 [THT]"]
  JP3 = Header 4 [package=1x04-smd]
  JP5 = Header 4 [package=1x04-smd]
  JP6 = Header 4 [package=1x04-smd]
  JP4 = Header 4 [package=1x04-smd]
  1M_pot = Resistor [tolerance=±5% resistance=220 package=THT]
  680pf = Ceramic Capacitor [capacitance=100nF package="100 mil [THT, multilayer]"]
  0_01uf = Ceramic Capacitor [capacitance=100nF package="100 mil [THT, multilayer]"]
  0_01uf_2 = Ceramic Capacitor [capacitance=100nF package="100 mil [THT, multilayer]"]
  ? = Ceramic Capacitor [capacitance=100nF package="100 mil [THT, multilayer]"]
  npn1 = NPN-Transistor [package="TO92 [THT]"]
  100k = Resistor [tolerance=±5% resistance=220 package=THT]
  100k_2 = Resistor [tolerance=±5% resistance=220 package=THT]
  0_01uf_3 = Ceramic Capacitor [capacitance=100nF package="100 mil [THT, multilayer]"]
  0_1uf = Ceramic Capacitor [capacitance=100nF package="100 mil [THT, multilayer]"]
  4069_cn = IC, DIP package, 14 pins [chip_label=IC]
  +9-12V = Battery
  100K_POt_RES = POT [package=pot_alpha_rv16af-20]
  U3 = POT [package=pot_alpha_rv16af-20]
  Dual_20k_pot_CUTOFF = POT [package=pot_alpha_rv16af-20]
  audio_in = Pad [width=2.39889411111112 height=2.257784 connect=center]
  0_1Uf = Tantalum Capacitor [capacitance=1μF package="100 mil [THT, tantalum]"]
  10K1 = Resistor [tolerance=±5% resistance=220 package=THT]
  10K2 = Resistor [tolerance=±5% resistance=220 package=THT]
  0_1Uf_2 = Tantalum Capacitor [capacitance=1μF package="100 mil [THT, tantalum]"]
  6_8k = Resistor [tolerance=±5% resistance=220 package=THT]
  out_BP = Pad [width=3.47350965943361 height=3.73402332149788 connect=center]
  IN_BP = Pad [width=3.47350965943361 height=3.73402332149788 connect=center]  # not connected
  out = Pad [width=3.47350965943361 height=3.73402332149788 connect=center]
  out2 = Pad [width=3.47350965943361 height=3.73402332149788 connect=center]
  out_keyboard = Pad [width=56.126273968610462 height=2.463514241186862 connect=center]
  output_selection_switch = SPST Switch [package=switch-spst-smd-a]

nets:
  N1: pot1.Pin_0, C1.0, IC1.pin1
  N2: pot1.Pin_1, IC1.pin2, IC1.pin3
  VSS: C1.1, VCC1.-, audio_out.Sleeve, audio_out.Ring, audio_out.Tip, IC1.pin5, IC1.pin7, IC1.pin13, C2.0, HEF1.Vss, HEF2.Vss, npn1.E, 0_01uf_3.1, 4069_cn.pin7, 4069_cn.pin9, 4069_cn.pin11, +9-12V.+, output_selection_switch.S
  VDD: VCC1.+, IC1.pin14, HEF1.Vdd, HEF2.Vdd, 4069_cn.pin14, +9-12V.-
  N3: IC1.pin4, HEF1.Q's, JP3.1
  N4: IC1.pin8, IC1.pin11, pot2.Pin_1
  N5: IC1.pin9, pot2.Pin_0, C2.1
  N6: IC1.pin10, HEF2.Q's
  N7: HEF1.DATA, JP4.4
  N8: HEF1.CLOCK, JP4.3
  N9: HEF1.Q2, JP4.2
  N10: HEF1.Q3, JP3.4
  N11: HEF1.Q4, JP3.3
  N12: HEF1.Qs, JP3.2
  N13: HEF2.DATA, JP5.4
  N14: HEF2.CLOCK, JP5.3
  N15: HEF2.Q2, JP5.2
  N16: HEF2.Q3, JP6.4
  N17: HEF2.Q4, JP6.3
  N18: HEF2.Qs, JP6.2
  N19: 1M_pot.Pin_0, 680pf.0
  N20: 1M_pot.Pin_1, 680pf.1, 0_01uf_2.0, ?.1
  N21: 0_01uf.0, 0_01uf_2.1, npn1.C
  N22: 0_01uf.1, 0_1uf.1, 4069_cn.pin12
  N23: 100k.Pin_0, 4069_cn.pin13
  N24: 100k.Pin_1, 100k_2.Pin_0, 0_01uf_3.0
  N25: 0_1uf.0, out_BP.pad
  N26: 4069_cn.pin1, 10K1.Pin_0, 10K2.Pin_0, 6_8k.Pin_0
  N27: 4069_cn.pin2, U3.A, 10K1.Pin_1
  N28: 4069_cn.pin3, U3.S, U3.E, 0_1Uf.-
  N29: 4069_cn.pin4, Dual_20k_pot_CUTOFF.A, 0_1Uf.+, out2.pad, output_selection_switch.O
  N30: 4069_cn.pin5, 0_1Uf_2.-
  N31: 4069_cn.pin6, 100K_POt_RES.S, 100K_POt_RES.E, 0_1Uf_2.+, out.pad, output_selection_switch.P
  N32: 100K_POt_RES.A, 6_8k.Pin_1
  N33: Dual_20k_pot_CUTOFF.S, Dual_20k_pot_CUTOFF.E
  N34: audio_in.pad, 10K2.Pin_1, out_keyboard.pad

notes:
  gnd
  cd4069 Bandpass filter
  0V
  cd4069 oscillating resonant lowpass filter
  2 octave synth and/or rythm
  cd4040
  cd40106
  2 octave pianosynth
  with resonant LP and BP filter/drumgen
