# Fritzing sketch id5_1232_0 (saved by Fritzing 0.9.2b)

parts:
  LCD1 = LCD screen
  Часть1 = Arduino Uno (Rev3)
  Matrix_keypad1 = CMG
  LCM1602_IIC1 = lcm.fzp [part_number="LCM1602 IIC" chip_label="LCM1602 IIC"]

nets:
  N1: LCD1.VSS, LCM1602_IIC1.connector0
  N2: LCD1.VDD, LCM1602_IIC1.connector1
  N3: LCD1.V0, LCM1602_IIC1.connector2
  N4: LCD1.RS, LCM1602_IIC1.connector3
  N5: LCD1.R/W, LCM1602_IIC1.connector4
  N6: LCD1.E, LCM1602_IIC1.connector5
  N7: LCD1.DB0, LCM1602_IIC1.connector6
  N8: LCD1.DB1, LCM1602_IIC1.connector7
  N9: LCD1.DB2, LCM1602_IIC1.connector8
  N10: LCD1.DB3, LCM1602_IIC1.connector9
  N11: LCD1.DB4, LCM1602_IIC1.connector10
  N12: LCD1.DB5, LCM1602_IIC1.connector11
  N13: LCD1.DB6, LCM1602_IIC1.connector12
  N14: LCD1.DB7, LCM1602_IIC1.connector13
  N15: LCD1.LED+, LCM1602_IIC1.connector14
  N16: LCD1.LED-, LCM1602_IIC1.connector15
  N17: Часть1.A4/SDA, LCM1602_IIC1.connector19
  N18: Часть1.A5/SCL, LCM1602_IIC1.connector18
  N19: Часть1.D8, Matrix_keypad1.connector27
  N20: Часть1.D9_PWM, Matrix_keypad1.connector26
  N21: Часть1.D10_PWM/SS, Matrix_keypad1.connector25
  N22: Часть1.D2, Matrix_keypad1.connector32
  N23: Часть1.D3_PWM, Matrix_keypad1.connector31
  N24: Часть1.D4, Matrix_keypad1.connector30
  N25: Часть1.D5_PWM, Matrix_keypad1.connector29
  N26: Часть1.D7, Matrix_keypad1.connector28
  N27: Часть1.5V, LCM1602_IIC1.connector17
  N28: Часть1.GND, LCM1602_IIC1.connector16
