# Fritzing sketch id600_Arduino_Servo_Motor_Control_With_PushButton_0 (saved by Fritzing 0.9.2b)
breadboards: 1

parts:
  Part1 = Arduino Uno (Rev3)
  S1 = Pushbutton [package="[THT]"]
  R1 = Resistor [tolerance=±5% resistance=1k package=THT]
  J1 = Basic Servo

nets:
  N1: Part1.D8, J1.pulse
  N2: Part1.D9_PWM, S1.Pin_1, S1.Pin_2, R1.Pin_0
  GND: Part1.GND, R1.Pin_1, J1.gnd
  N3: Part1.3V3, S1.Pin_3, S1.Pin_4
  5V: Part1.5V, J1.vcc
