# Fritzing sketch id601_qq_0 (saved by Fritzing 0.9.1b)
circuit board: 6.88566cm x 5.36311cm

parts:
  J1 = double row female pin header, 8 pins [form="♀ (female)"]
  J2 = female pin header, 4 pins [form="♀ (female)"]
  J3 = female pin header, 4 pins [form="♀ (female)"]
  J4 = female pin header, 4 pins [form="♀ (female)"]
  J5 = female pin header, 4 pins [form="♀ (female)"]
  J6 = female pin header, 4 pins [form="♀ (female)"]
  Part1 = Arduino Uno (Rev3) - ICSP
  J7 = double row female pin header, 12 pins [form="♀ (female)"]
  J8 = female pin header, 6 pins [form="♀ (female)"]
  J9 = double row female pin header, 12 pins [form="♀ (female)"]
  J10 = female pin header, 6 pins [form="♀ (female)"]
  J11 = double row female pin header, 12 pins [form="♀ (female)"]
  J12 = female pin header, 6 pins [form="♀ (female)"]
  J13 = double row female pin header, 8 pins [form="♀ (female)"]
  J14 = double row female pin header, 8 pins [form="♀ (female)"]
  J15 = female pin header, 4 pins [form="♀ (female)"]
  J16 = female pin header, 6 pins [form="♀ (female)"]
  J17 = female pin header, 6 pins [form="♀ (female)"]
  MIRF1 = MIRF [package=mirf]  # not connected
  R1 = Resistor [tolerance=±5% resistance=220 package=THT]
  J18 = female pin header, 2 pins [form="♀ (female)"]

nets:
  N1: J1.pin1, J1.pin2, J1.pin3, J1.pin4, J3.pin3, J4.pin3, J5.pin3, J6.pin3, Part1.5V, J8.pin1, J8.pin2, J8.pin3, J8.pin4, J8.pin5, J8.pin6, J10.pin1, J10.pin2, J10.pin3, J10.pin4, J10.pin5, J10.pin6, J12.pin1, J12.pin2, J12.pin3, J12.pin4, J12.pin5, J12.pin6
  N2: J1.pin5, J1.pin6, J1.pin7, J1.pin8, J3.pin4, J4.pin4, J5.pin4, J6.pin4, Part1.GND, J7.pin7, J7.pin8, J7.pin9, J7.pin10, J7.pin11, J7.pin12, J9.pin1, J9.pin2, J9.pin3, J9.pin4, J9.pin5, J9.pin6, J11.pin1, J11.pin2, J11.pin3, J11.pin4, J11.pin5, J11.pin6, J13.pin4, J16.pin3, J18.pin1
  N3: J2.pin1, J2.pin2, J2.pin3, J2.pin4, Part1.3V3, J13.pin8, J16.pin2, R1.Pin_1
  N4: J3.pin1, J4.pin1, J5.pin1, J6.pin1, Part1.A5/SCL, J7.pin6, J17.pin5
  N5: J3.pin2, J4.pin2, J5.pin2, J6.pin2, Part1.A4/SDA, J7.pin5, J17.pin4
  N6: Part1.A0, J7.pin1
  N7: Part1.A1, J7.pin2
  N8: Part1.A2, J7.pin3
  N9: Part1.A3, J7.pin4
  N10: Part1.ICSP_MISO, Part1.D12/MISO, J9.pin11, J14.pin1, J14.pin2, J14.pin3, J14.pin4, J16.pin5, J17.pin2, J17.pin6
  N11: Part1.ICSP_SCK, Part1.D13/SCK, J9.pin12, J15.pin1, J15.pin2, J15.pin3, J15.pin4, J16.pin1, J16.pin4, J17.pin1
  N12: Part1.ICSP_MOSI, Part1.D11_PWM/MOSI, J9.pin10, J14.pin5, J14.pin6, J14.pin7, J14.pin8, J16.pin6, J17.pin3
  N13: Part1.D8, J9.pin7
  N14: Part1.D9_PWM, J9.pin8
  N15: Part1.D10_PWM/SS, J9.pin9
  N16: Part1.D2, J11.pin7
  N17: Part1.D3_PWM, J11.pin8
  N18: Part1.D4, J11.pin9
  N19: Part1.D5_PWM, J11.pin10, J13.pin5
  N20: Part1.D6_PWM, J11.pin11
  N21: Part1.D7, J11.pin12, J13.pin1
  N22: R1.Pin_0, J18.pin2
