# Fritzing sketch id602_wifiCamera_0 (saved by Fritzing 0.8.7b)

parts:
  Componente1 = Arduino Uno (Rev3)  # not connected
  Componente2 = Arduino Prototyping Shield
  CC3K1 = Adafruit_CC3000_WiFi_Breakout
  CAMERA1 = TTL_Serial_JPEG_Camera
  R1 = Resistor [tolerance=±5% resistance=10k package=THT]
  R2 = Resistor [tolerance=±5% resistance=10k package=THT]

nets:
  N1: Componente2.+5V, Componente2.N$77, CC3K1.connector3, CAMERA1.connector6
  N2: Componente2.GND, Componente2.N$118, Componente2.N$393, CC3K1.connector1, CAMERA1.connector5, R2.Pin_1
  N3: Componente2.D10, Componente2.N$48, CC3K1.connector7
  N4: Componente2.D11, Componente2.N$62, CC3K1.connector6
  N5: Componente2.D12, Componente2.N$72, CC3K1.connector5
  N6: Componente2.D13, Componente2.N$86, CC3K1.connector4
  N7: Componente2.D2, R1.Pin_0
  N8: Componente2.D3, Componente2.N$27, CC3K1.connector9
  N9: Componente2.D4, CAMERA1.connector3
  N10: Componente2.D5, Componente2.N$37, CC3K1.connector8
  N11: Componente2.N$76, CC3K1.connector2
  N12: Componente2.N$405, CAMERA1.connector4, R2.Pin_0
  N13: Componente2.N$406, R1.Pin_1
