# Fritzing sketch id603_myBlinkyPCB_0 (saved by Fritzing 0.9.2b)
circuit board: 6.86441cm x 5.37903cm
breadboards: 1

parts:
  EEPROM = IC, DIP package, 8 pins [chip_label=IC]
  IC2 = IC, DIP package, 16 pins [chip_label=IC]
  SRAM = IC, DIP package, 8 pins [chip_label=IC]
  Part1 = Arduino Uno (Rev3) - ICSP

nets:
  N1: EEPROM.pin1, IC2.pin10
  N2: EEPROM.pin2, SRAM.pin2, Part1.ICSP_MISO, Part1.D12/MISO
  N3: EEPROM.pin3, EEPROM.pin7, EEPROM.pin8, IC2.pin1, SRAM.pin7, SRAM.pin8, Part1.3V3
  N4: EEPROM.pin4, IC2.pin8, SRAM.pin4, Part1.GND
  N5: EEPROM.pin5, IC2.pin15, SRAM.pin5
  N6: EEPROM.pin6, IC2.pin6, SRAM.pin6
  N7: IC2.pin7, Part1.ICSP_SCK, Part1.D13/SCK
  N8: IC2.pin9, Part1.A5/SCL
  N9: IC2.pin11, Part1.D10_PWM/SS
  N10: IC2.pin12, SRAM.pin1
  N11: IC2.pin14, Part1.ICSP_MOSI, Part1.D11_PWM/MOSI

notes:
  blinkyBasic :]
