# Fritzing sketch id604_arduino_shield_rtc_0 (saved by Fritzing 0.9.3b)
circuit board: 8.32995cm x 10.9854cm
breadboards: 1

parts:
  Hours = Arduino Uno (Rev3)
  IC1 = DS1307 [package=THT]
  R1 = Resistor [tolerance=±5% resistance=220 package=THT]
  R2 = Resistor [tolerance=±5% resistance=220 package=THT]
  R3 = Resistor [tolerance=±5% resistance=220 package=THT]
  R4 = Resistor [tolerance=±5% resistance=220 package=THT]
  R5 = Resistor [tolerance=±5% resistance=220 package=THT]
  R6 = Resistor [tolerance=±5% resistance=220 package=THT]
  R7 = Resistor [tolerance=±5% resistance=220 package=THT]
  R8 = Resistor [tolerance=±5% resistance=220 package=THT]
  R9 = Resistor [tolerance=±5% resistance=220 package=THT]
  minutes = Battery Holders [package=battcom_20mm_pth]
  R11 = Resistor [tolerance=±5% resistance=1k package=THT]
  R12 = Resistor [tolerance=±5% resistance=1k package=THT]
  XTAL1 = CRYSTAL - kHz [frequency="32 MHz"]
  R10 = Resistor [tolerance=±5% resistance=220 package=THT]
  1 = LED - 3mm [color="Red (633nm)" package="3 mm [THT]"]
  2 = LED - 3mm [color="Red (633nm)" package="3 mm [THT]"]
  3 = LED - 3mm [color="Red (633nm)" package="3 mm [THT]"]
  7 = LED - 3mm [color="Red (633nm)" package="3 mm [THT]"]
  +10 = LED - 3mm [color="Green (560nm)" package="3 mm [THT]"]
  +5 = LED - 3mm [color="Yellow (592nm)" package="3 mm [THT]"]
  0 = LED - 3mm [color="Blue (470nm)" package="3 mm [THT]"]
  15 = LED - 3mm [color="Blue (470nm)" package="3 mm [THT]"]
  30 = LED - 3mm [color="Blue (470nm)" package="3 mm [THT]"]
  45 = LED - 3mm [color="Blue (470nm)" package="3 mm [THT]"]
  S1 = Pushbutton [package="[THT]"]

nets:
  N1: Hours.A4/SDA, IC1.SDA_-_I2C_Data, R11.Pin_1
  N2: Hours.A5/SCL, IC1.SCL_-_I2C_Clock, R12.Pin_1
  N3: Hours.D8, +10.cathode
  N4: Hours.D9_PWM, +5.cathode
  N5: Hours.D10_PWM/SS, 0.cathode
  N6: Hours.D11_PWM/MOSI, 15.cathode
  N7: Hours.D12/MISO, 30.cathode
  N8: Hours.D13/SCK, 45.cathode
  N9: Hours.D2, S1.Pin_3, S1.Pin_4
  N10: Hours.D3_PWM, IC1.SWQ/OUT_-_Clock_Output
  N11: Hours.D4, 2.cathode
  N12: Hours.D5_PWM, 1.cathode
  N13: Hours.D6_PWM, 7.cathode
  N14: Hours.D7, 3.cathode
  N15: Hours.5V, IC1.+V, R11.Pin_0, R12.Pin_0
  N16: Hours.GND, IC1.0V, R1.Pin_1, R2.Pin_1, R3.Pin_1, R4.Pin_1, R5.Pin_1, R6.Pin_1, R7.Pin_1, R8.Pin_1, R9.Pin_1, minutes.-, R10.Pin_1, S1.Pin_1, S1.Pin_2
  N17: IC1.X1_-_Crystal, XTAL1.pin_1
  N18: IC1.X2_-_Crystal, XTAL1.pin_0
  N19: IC1.Vbat_-_Backup_Supply, minutes.+
  N20: R1.Pin_0, 1.anode
  N21: R2.Pin_0, 2.anode
  N22: R3.Pin_0, 3.anode
  N23: R4.Pin_0, 7.anode
  N24: R5.Pin_0, +10.anode
  N25: R6.Pin_0, +5.anode
  N26: R7.Pin_0, 0.anode
  N27: R8.Pin_0, 15.anode
  N28: R9.Pin_0, 30.anode
  N29: R10.Pin_0, 45.anode
