# Fritzing sketch id605_DS1307_SHIELD_v3_0 (saved by Fritzing 0.7.7b)
breadboards: 1

parts:
  LED1 = smd LED [color="Red (633nm)" package="0603 [SMD]"]
  R1 = Resistor [tolerance=±5% resistance=220 package=THT]
  IC_DS1307 = DS1307 [package=THT]
  R2 = Resistor [tolerance=±5% resistance=4.7k package=THT]
  R3 = Resistor [tolerance=±5% resistance=4.7k package=THT]
  CR2032_-_3V_Battery = LilyPad Coin Cell Battery Holder [part_number="for CR2032 cell"]
  Arduino1 = Arduino
  Quartz_32768khz = Ceramic Capacitor [capacitance=100nF package="100 mil [THT, multilayer]"]
  24LC32 = 24LC01 [package=THT]
  C5 = Ceramic Capacitor [capacitance=100nF package="100 mil [THT, multilayer]"]
  DS1621 = IC, DIP package, 8 pins [chip_label=DS1621]
  C6 = Ceramic Capacitor [capacitance=100nF package="100 mil [THT, multilayer]"]
  C3 = Ceramic Capacitor [capacitance=100nF package="200 mil [THT, multilayer]"]
  Write_Protect = female pin header, 2 pins [form="♀ (female)"]
  J2 = female pin header, 4 pins [form="♀ (female)"]
  J4 = female pin header, 4 pins [form="♀ (female)"]
  J5 = female pin header, 4 pins [form="♀ (female)"]
  J6 = female pin header, 4 pins [form="♀ (female)"]

nets:
  N1: LED1.cathode, IC_DS1307.SWQ/OUT_-_Clock_Output
  N2: LED1.anode, R1.Pin_1
  N3: R1.Pin_0, IC_DS1307.+V, R2.Pin_0, R3.Pin_0, Arduino1.+5V, 24LC32.+V, C5.1, DS1621.pin8, C6.0, C3.1, Write_Protect.pin2, J2.pin1, J4.pin1, J5.pin1, J6.pin1
  N4: IC_DS1307.X1_-_Crystal, Quartz_32768khz.1
  N5: IC_DS1307.X2_-_Crystal, Quartz_32768khz.0
  N6: IC_DS1307.Vbat_-_Backup_Supply, CR2032_-_3V_Battery.+
  N7: IC_DS1307.0V, CR2032_-_3V_Battery.-, Arduino1.GND, 24LC32.A0, 24LC32.A1, 24LC32.A2, 24LC32.0V, C5.0, DS1621.pin4, DS1621.pin5, DS1621.pin6, DS1621.pin7, C6.1, C3.0, J2.pin3, J4.pin3, J5.pin3, J6.pin3
  N8: IC_DS1307.SDA_-_I2C_Data, R3.Pin_1, Arduino1.A4, Arduino1.SDA, 24LC32.SDA_-_I2C_Data, DS1621.pin1, J2.pin2, J4.pin2, J5.pin2, J6.pin2
  N9: IC_DS1307.SCL_-_I2C_Clock, R2.Pin_1, Arduino1.A5, Arduino1.SCL, 24LC32.SCL_-_I2C_Clock, DS1621.pin2, J2.pin4, J4.pin4, J5.pin4, J6.pin4
  N10: 24LC32.WP_-_Write_Protect, Write_Protect.pin1

notes:
  Crystal: 32. 768 Khz
  1K Ohm Resistors
  Backup Battery CR2032 ( >8 years)
  DS1307, 24LC32, DS1621, Arduino Shield for RTC, EEPROM, TEMP, this shield is compatible with Amicus18 - Tested OK., v1
  PORT i2c
  QUARTZ 32768Khz
