# Fritzing sketch id606_CIRC05_SimpleSensorLarson_0 (saved by Fritzing 0.7.9b)
breadboards: 1

parts:
  U1 = 74HC595 [package="DIP16 [THT]"]
  LED7 = LED - 5mm [color="Red (633nm)" package="5 mm [THT]"]
  LED6 = LED - 5mm [color="Red (633nm)" package="5 mm [THT]"]
  LED5 = LED - 5mm [color="Red (633nm)" package="5 mm [THT]"]
  LED4 = LED - 5mm [color="Red (633nm)" package="5 mm [THT]"]
  LED3 = LED - 5mm [color="Red (633nm)" package="5 mm [THT]"]
  LED2 = LED - 5mm [color="Red (633nm)" package="5 mm [THT]"]
  LED1 = LED - 5mm [color="Red (633nm)" package="5 mm [THT]"]
  LED0 = LED - 5mm [color="Red (633nm)" package="5 mm [THT]"]
  R6 = Resistor [tolerance=±5% resistance=330 package=THT]
  R5 = Resistor [tolerance=±5% resistance=330 package=THT]
  R4 = Resistor [tolerance=±5% resistance=330 package=THT]
  R3 = Resistor [tolerance=±5% resistance=330 package=THT]
  R2 = Resistor [tolerance=±5% resistance=330 package=THT]
  R1 = Resistor [tolerance=±5% resistance=330 package=THT]
  R0 = Resistor [tolerance=±5% resistance=330 package=THT]
  R7 = Resistor [tolerance=±5% resistance=330 package=THT]
  POT1 = Rotary Potentiometer (Small) [maximum_resistance=100kΩ]
  Arduino1 = Arduino
  SW1 = IC, DIP package, 8 pins [chip_label="DIP Switch"]

nets:
  N1: U1.Q1, LED1.anode
  N2: U1.Q2, LED2.anode
  N3: U1.Q3, LED3.anode
  N4: U1.Q4, LED4.anode
  N5: U1.Q5, LED5.anode
  N6: U1.Q6, LED6.anode
  N7: U1.Q7, LED7.anode
  GND: U1.GND, U1.OE, R6.Pin_1, R5.Pin_1, R4.Pin_1, R3.Pin_1, R2.Pin_1, R1.Pin_1, R0.Pin_1, R7.Pin_1, POT1.leg1, Arduino1.GND, SW1.pin5, SW1.pin6, SW1.pin7, SW1.pin8
  5V: U1.MR, U1.VCC, POT1.leg2, Arduino1.+5V
  SerClk: U1.SH_CP, Arduino1.D3
  SerLatch: U1.ST_CP, Arduino1.D4
  SerData: U1.DS, Arduino1.D2
  N8: U1.Q0, LED0.anode
  N9: LED7.cathode, R7.Pin_0
  N10: LED6.cathode, R6.Pin_0
  N11: LED5.cathode, R5.Pin_0
  N12: LED4.cathode, R4.Pin_0
  N13: LED3.cathode, R3.Pin_0
  N14: LED2.cathode, R2.Pin_0
  N15: LED1.cathode, R1.Pin_0
  N16: LED0.cathode, R0.Pin_0
  TimingAdj: POT1.wiper, Arduino1.A0
  DIPpin[0]: Arduino1.D13, SW1.pin1
  DIPpin[1]: Arduino1.D12, SW1.pin2
  DIPpin[2]: Arduino1.D11, SW1.pin3
  DIPpin[3]: Arduino1.D10, SW1.pin4

notes:
  Larson Scanner with input for timing and width using a 74HC595 shift register.
  Based on ARDX Circuit 05. http://ardx.org/CIRC05
  Layout by Chris "Sembazuru" Elliott
  ARDX Circuit 5 expansion, Larson Scanner with input for timing and width, 1.1
  Larson Scanner with input for timing and width
  Sembazuru
  Circuits
