# Fritzing sketch id607_Arduino_Solar_panel_tracker_0 (saved by Fritzing 0.8.7b)
breadboards: 1

parts:
  VCC1 = Battery block 9V
  Part1 = Arduino Uno (Rev3) - ICSP
  R1 = Resistor [tolerance=±5% resistance=220 package=THT]
  R2 = Resistor [package="2010 [SMD]"]
  R3 = Photocell (LDR) [package=THT]
  R4 = Photocell (LDR) [package=THT]
  D1 = SOLAR-IXYS [package=solarbit-12x1]  # not connected
  J1 = Basic Servo

nets:
  GND: VCC1.-, Part1.GND, R1.Pin_0, R2.Pin_1, J1.gnd
  N1: VCC1.+, Part1.VIN
  N2: Part1.A0, R1.Pin_1, R3.pin_1
  N3: Part1.A1, R2.Pin_0, R4.pin_0
  N4: Part1.D9_PWM, J1.pulse
  5V: Part1.5V, R3.pin_0, R4.pin_1, J1.vcc
