# Fritzing sketch id608_Untitled_Sketch_0 (saved by Fritzing 0.9.3b)
perfboards: 1

parts:
  Componente1 = Arduino Uno (Rev3)
  Componente2 = EasyDriver_v44
  Componente3 = EasyDriver_v44
  M1 = Stepper Motor - Unipolar
  M2 = Stepper Motor - Unipolar
  R3 = Photocell (LDR) [package=THT]  # not connected
  R4 = Photocell (LDR) [package=THT]  # not connected
  R6 = Photocell (LDR) [package=THT]  # not connected
  R7 = Photocell (LDR) [package=THT]  # not connected
  R8 = Resistor [tolerance=±5% resistance=220 package="1206 [SMD]"]  # not connected
  Power_plug1 = Power plug  # not connected
  M3 = Dagu DGServo 9g (Top view) [part_number=RS001B]
  M4 = Dagu DGServo 9g (Top view) [part_number=RS001B]
  R9 = Trimmer Potentiometer [maximum_resistance=10kΩ package=THT]
  R10 = Trimmer Potentiometer [maximum_resistance=10kΩ package=THT]
  R11 = Resistor [tolerance=±5% resistance=220 package="1206 [SMD]"]  # not connected
  R12 = Resistor [tolerance=±5% resistance=220 package="1206 [SMD]"]  # not connected
  R13 = Resistor [tolerance=±5% resistance=220 package="1206 [SMD]"]  # not connected

nets:
  N1: Componente1.A2, R9.wiper
  N2: Componente1.A3, R10.wiper
  N3: Componente1.D8, M3.pulse
  N4: Componente1.D9_PWM, M4.gnd, M4.pulse
  GND: Componente1.GND, Componente2.GND, Componente3.GND
  N5: Componente1.D2, Componente3.DIR
  N6: Componente1.D3_PWM, Componente3.STEP
  N7: Componente1.D4, Componente2.DIR
  N8: Componente1.D5_PWM, Componente2.STEP
  N9: Componente2.V+, Componente3.V+
  N10: Componente2.OUT2A, M2.A
  N11: Componente2.OUT2B, M2.C
  N12: Componente2.OUT1A, M2.B
  N13: Componente2.OUT1B, M2.D
  N14: Componente3.OUT2A, M1.A
  N15: Componente3.OUT2B, M1.C
  N16: Componente3.OUT1A, M1.B
  N17: Componente3.OUT1B, M1.D

notes:
  Asse Y - Inclina il pannello
  Asse X - Ruota il pannello
