# Fritzing sketch id609_Arduino_radar_sonar_progetto_hc_sr04_0 (saved by Fritzing 0.9.2b)
breadboards: 1

parts:
  U3 = generic_sip_4_300mil.fzp [chip_label=IC]
  Componente1 = Arduino Uno (Rev3)
  J1 = Basic Servo

nets:
  5V: U3.connector0, Componente1.5V, J1.vcc
  N1: U3.connector1, Componente1.D10_PWM/SS
  N2: U3.connector2, Componente1.D11_PWM/MOSI
  GND: U3.connector3, Componente1.GND, J1.gnd
  N3: Componente1.D12/MISO, J1.pulse
