# Fritzing sketch id610_Untitled_Sketch_0 (saved by Fritzing 0.9.3b)
breadboards: 1

parts:
  Part1 = Arduino Uno (Rev3)
  J1 = Basic Servo
  hc-sr1 = hc-sr04

nets:
  N1: Part1.D10_PWM/SS, hc-sr1.Trig
  N2: Part1.D11_PWM/MOSI, hc-sr1.Echo
  VCC: Part1.5V, J1.vcc, hc-sr1.VCC
  GND: Part1.GND, J1.gnd, hc-sr1.GND
