# Fritzing sketch id612_StandAlone328_0 (saved by Fritzing 0.7.12b)

parts:
  C1 = Ceramic Disk Capacitor [package=THT]
  R1 = 1k Ω Resistor [package=THT]
  C2 = Ceramic Disk Capacitor [package=THT]
  S1 = Pushbutton [package="[THT]"]
  XTAL1 = Crystal [frequency="16 Mhz" package=SMD]
  Arduino_StandAlone_By_FLPRO = atmega328 [package=dip]
  U2 = Mystery Part - 6 pins [package=THT]
  U3 = Mystery Part - 5 pins [package=THT]
  U4 = Mystery Part - 4 pins [package=THT]
  U5 = Mystery Part - 5 pins [package=THT]

nets:
  N1: C1.pin_0, XTAL1.pin_1, Arduino_StandAlone_By_FLPRO.XLAT1
  N2: C1.pin_1, C2.pin_0, Arduino_StandAlone_By_FLPRO.GND
  N3: R1.Pin_0, S1.Pin_1, S1.Pin_2, Arduino_StandAlone_By_FLPRO.VCC, Arduino_StandAlone_By_FLPRO.AVCC
  N4: R1.Pin_1, Arduino_StandAlone_By_FLPRO.RESET
  N5: C2.pin_1, XTAL1.pin_0, Arduino_StandAlone_By_FLPRO.XLAT2
  N6: Arduino_StandAlone_By_FLPRO.D0_(RX), U5.leg5
  N7: Arduino_StandAlone_By_FLPRO.D1_(TX), U5.leg4
  N8: Arduino_StandAlone_By_FLPRO.D2, U5.leg3
  N9: Arduino_StandAlone_By_FLPRO.D3_(PWM), U5.leg2
  N10: Arduino_StandAlone_By_FLPRO.D4, U5.leg1
  N11: Arduino_StandAlone_By_FLPRO.D5_(PWM), U4.leg4
  N12: Arduino_StandAlone_By_FLPRO.D6_(PWM), U4.leg3
  N13: Arduino_StandAlone_By_FLPRO.D7, U4.leg2
  N14: Arduino_StandAlone_By_FLPRO.D8, U4.leg1
  N15: Arduino_StandAlone_By_FLPRO.D9_(PWM), U3.leg5
  N16: Arduino_StandAlone_By_FLPRO.D10_(PWM), U3.leg4
  N17: Arduino_StandAlone_By_FLPRO.D11_(PWM), U3.leg3
  N18: Arduino_StandAlone_By_FLPRO.D12, U3.leg2
  N19: Arduino_StandAlone_By_FLPRO.D13, U3.leg1
  N20: Arduino_StandAlone_By_FLPRO.A0, U2.leg6
  N21: Arduino_StandAlone_By_FLPRO.A1, U2.leg5
  N22: Arduino_StandAlone_By_FLPRO.A2, U2.leg4
  N23: Arduino_StandAlone_By_FLPRO.A3, U2.leg3
  N24: Arduino_StandAlone_By_FLPRO.A4, U2.leg2
  N25: Arduino_StandAlone_By_FLPRO.A5, U2.leg1
