# Fritzing sketch id613_KitProject7Plus_0 (saved by Fritzing 0.9.0b)
circuit board: 6.88566cm x 5.36311cm
breadboards: 1

parts:
  Part1 = Arduino Uno (Rev3)
  J1 = Piezo Speaker
  S1 = Pushbutton [package="[THT]"]
  S2 = Pushbutton [package="[THT]"]
  S3 = Pushbutton [package="[THT]"]
  S4 = Pushbutton [package="[THT]"]
  R1 = Resistor [tolerance=±10% resistance=10k package=THT]
  R2 = Resistor [tolerance=±10% resistance=220 package=THT]
  R3 = Resistor [tolerance=±10% resistance=10k package=THT]
  R4 = Resistor [tolerance=±10% resistance=10k package=THT]
  R5 = Resistor [tolerance=±10% resistance=10k package=THT]
  R6 = Resistor [tolerance=±10% resistance=10k package=THT]

nets:
  N1: Part1.A0, S1.Pin_1, S1.Pin_2, S2.Pin_1, S2.Pin_2, S3.Pin_1, S3.Pin_2, S4.Pin_1, S4.Pin_2, R1.Pin_1
  N2: Part1.D8, J1.pin2
  N3: Part1.GND, J1.pin1, R1.Pin_0
  N4: Part1.5V, S1.Pin_3, S1.Pin_4, R2.Pin_0, R3.Pin_0, R4.Pin_0
  N5: S2.Pin_3, S2.Pin_4, R2.Pin_1
  N6: S3.Pin_3, S3.Pin_4, R3.Pin_1
  N7: S4.Pin_3, S4.Pin_4, R6.Pin_0
  N8: R4.Pin_1, R5.Pin_0
  N9: R5.Pin_1, R6.Pin_1

notes:
  This circuit is a slight modification of the Arduino Starter Kit project 07: Keyboard Instrument: http://arduino.cc/en/Main/ArduinoStarterKit
  The original uses a 1Mohm resistor. That resistor value produces pin 8 values that are too close to zero, which causes the output to crackle as if that switch were unreliable.
  In this circuit, the 1Mohm resistor is replaced by a 30Kohm resistor. Actually, by 3 10Kohm resistors in series, to produce 30Kohm. This resistor value produces pin 8 values that are nicely between zero and the value from the next pushbutton.
  Note the 3 10K resistors in series. I did that because the Arduino Starter Kit has no 30K resistors, but has plenty of 10K resistors.
