# Fritzing sketch id614_a4988_stepper_0 (saved by Fritzing 0.9.3b)
breadboards: 1

parts:
  Part1 = Arduino Uno (Rev3)
  S1 = Momentary Switch [package=ksa_sealed_tac_switch]
  S2 = Momentary Switch [package=ksa_sealed_tac_switch]
  M1 = Stepper Motor - Bipolar
  Power_plug1 = Power plug
  Pololu_A1 = Pololu A4988 [package=SO16]

nets:
  N1: Part1.D8, Pololu_A1.DIR
  N2: Part1.D9_PWM, Pololu_A1.STEP
  GND: Part1.GND, S1.3, S1.4, S2.3, S2.4, Power_plug1.GND, Pololu_A1.GND
  N3: Part1.D2, S1.1, S1.2
  N4: Part1.D3_PWM, S2.1, S2.2
  5V: Part1.5V, Pololu_A1.VDD
  VIN: Part1.VIN, Power_plug1.VCC, Pololu_A1.VMOT
  N5: M1.A, Pololu_A1.1B
  N6: M1.C, Pololu_A1.1A
  N7: M1.B, Pololu_A1.2A
  N8: M1.D, Pololu_A1.2B
  N9: Pololu_A1.RESET, Pololu_A1.SLEEP
