# Fritzing sketch id615_cnc_0 (saved by Fritzing 0.9.1b)
breadboards: 1
perfboards: 1

parts:
  Part1 = Arduino Uno (Rev3)  # not connected
  Part2 = Arduino Motor Shield (Rev3)
  U1 = Thumb Joystick [package=joystick]  # not connected
  M1 = Stepper Motor - Bipolar

nets:
  N1: Part2.B-, M1.D
  N2: Part2.B+, M1.B
  N3: Part2.A-, M1.C
  N4: Part2.A+, M1.A
