# Fritzing sketch id617_stop_watch_0 (saved by Fritzing 0.9.3b)
breadboards: 1

parts:
  S1 = Pushbutton [package="[THT]"]
  S2 = Pushbutton [package="[THT]"]
  LCD1 = LCD screen
  Part1 = Arduino Uno (Rev3)
  R1 = Rotary Potentiometer (Small) [maximum_resistance=100kΩ package=THT]
  R2 = Resistor [tolerance=±5% resistance=1k package=THT]

nets:
  N1: S1.Pin_1, S1.Pin_2, Part1.D9_PWM
  VSS: S1.Pin_3, S1.Pin_4, S2.Pin_3, S2.Pin_4, LCD1.VSS, LCD1.R/W, Part1.GND, R1.leg1, R2.Pin_0
  N2: S2.Pin_1, S2.Pin_2, Part1.D8
  VDD: LCD1.VDD, LCD1.LED+, Part1.5V, R1.leg2
  N3: LCD1.V0, R1.wiper
  N4: LCD1.RS, Part1.D7
  N5: LCD1.E, Part1.D6_PWM
  N6: LCD1.DB4, Part1.D5_PWM
  N7: LCD1.DB5, Part1.D4
  N8: LCD1.DB6, Part1.D3_PWM
  N9: LCD1.DB7, Part1.D2
  N10: LCD1.LED-, R2.Pin_1
