# Fritzing sketch id618_1electrical_project_0 (saved by Fritzing 0.9.3b)
breadboards: 1

parts:
  Matrix_keypad1 = CMG
  R1 = Resistor [tolerance=±5% resistance=1k package="0402 [SMD]"]
  R2 = Resistor [tolerance=±5% resistance=1k package="0402 [SMD]"]
  R3 = Resistor [tolerance=±5% resistance=1k package="0402 [SMD]"]
  R4 = Resistor [tolerance=±5% resistance=220 package="0402 [SMD]"]
  R5 = Resistor [tolerance=±5% resistance=1k package="0402 [SMD]"]
  R6 = Resistor [tolerance=±5% resistance=220 package="0402 [SMD]"]
  R7 = Resistor [tolerance=±5% resistance=220 package="0402 [SMD]"]
  R8 = Resistor [tolerance=±5% resistance=10 package="0402 [SMD]"]
  Part1 = Arduino Uno (Rev3)
  U2 = LCD-16X2 [package=lcd-16x2_noholes]
  U3 = POT [package=pot_alpha_rv16af-20]
  U4 = L298 [package=multiwatt15_6400bgheatsink]
  M1 = DC Motor  # not connected
  J1 = Infrared Proximity Sensor
  VCC1 = Battery block 9V

nets:
  N1: Matrix_keypad1.connector25, R1.Pin_0, R2.Pin_1
  N2: Matrix_keypad1.connector26, R2.Pin_0, R3.Pin_1
  N3: Matrix_keypad1.connector27, R3.Pin_0, R5.Pin_1
  N4: Matrix_keypad1.connector28, R5.Pin_0
  N5: Matrix_keypad1.connector29, R4.Pin_1, R8.Pin_1, Part1.A5/SCL
  N6: Matrix_keypad1.connector30, R4.Pin_0, R6.Pin_1
  N7: Matrix_keypad1.connector31, R6.Pin_0, R7.Pin_1
  N8: Matrix_keypad1.connector32, R7.Pin_0
  5V: R1.Pin_1, Part1.5V, U2.VDD, U3.A, U4.CSA, J1.Vcc
  GND: R8.Pin_0, Part1.GND, U2.R_W, U3.E, U4.IN4, J1.GND, VCC1.-
  N9: Part1.D10_PWM/SS, U2.DB4
  N10: Part1.D11_PWM/MOSI, U2.DB5
  N11: Part1.D12/MISO, U2.DB6
  N12: Part1.D13/SCK, U2.DB7
  N13: Part1.D4, U2.RS
  N14: Part1.D5_PWM, U4.OUT1
  N15: Part1.D6_PWM, U4.OUT2
  N16: Part1.D7, U2.E
  N17: U2.VO, U3.S
  N18: U4.OUT3, VCC1.+
