# Fritzing sketch id619_Telegraph_Sketch_0 (saved by Fritzing 0.9.0b)
breadboards: 2

parts:
  R3 = Resistor [tolerance=±5% resistance=220 package=THT]
  S5 = Pushbutton [package=THT]
  Part3 = Arduino Uno (Rev3)
  S1 = Pushbutton [package=THT]
  R4 = Resistor [tolerance=±5% resistance=220 package=THT]
  R1 = Resistor [tolerance=±5% resistance=220 package=THT]
  S4 = Pushbutton [package=THT]
  S3 = Pushbutton [package=THT]
  R2 = Resistor [tolerance=±5% resistance=220 package=THT]
  Part2 = Arduino Uno (Rev3)
  S6 = Pushbutton [package=THT]
  R5 = Resistor [tolerance=±5% resistance=220 package=THT]
  R6 = Resistor [tolerance=±5% resistance=220 package=THT]
  S2 = Pushbutton [package=THT]

nets:
  N1: R3.Pin_0, S3.leg0, Part2.D11_PWM/MOSI
  GND: R3.Pin_1, Part3.GND, R4.Pin_1, R1.Pin_1, R2.Pin_1, Part2.GND, R5.Pin_1, R6.Pin_1
  N2: S5.leg0, Part3.D8, R5.Pin_0
  N3: S5.leg1, Part3.5V, S4.leg1, S6.leg1
  N4: Part3.D9_PWM, Part2.D10_PWM/SS
  N5: Part3.D10_PWM/SS, Part2.D9_PWM
  N6: Part3.D11_PWM/MOSI, S6.leg0, R6.Pin_0
  N7: Part3.D2, R4.Pin_0, S4.leg0
  N8: S1.leg0, R1.Pin_0, Part2.D2
  N9: S1.leg1, S3.leg1, Part2.5V, S2.leg1
  N10: R2.Pin_0, Part2.D8, S2.leg0
