# Fritzing sketch id621_temp_sensor_with_lcd_2_0 (saved by Fritzing 0.9.0b)
breadboards: 1

parts:
  LCD1 = LCD screen
  Part1 = Arduino Uno (Rev3)
  R2 = Rotary Potentiometer (Small) [maximum_resistance=10kΩ package=THT]
  T1 = LM35 Temperature Sensor [package="TO92 [THT]"]

nets:
  GND: LCD1.VSS, LCD1.R/W, LCD1.LED-, Part1.GND, R2.leg1, T1.GND
  VDD: LCD1.VDD, LCD1.LED+, Part1.5V, R2.leg2, T1.+Vs
  N1: LCD1.V0, R2.wiper
  N2: LCD1.RS, Part1.D7
  N3: LCD1.E, Part1.D8
  N4: LCD1.DB4, Part1.D9_PWM
  N5: LCD1.DB5, Part1.D10_PWM/SS
  N6: LCD1.DB6, Part1.D11_PWM/MOSI
  N7: LCD1.DB7, Part1.D12/MISO
  N8: Part1.A1, T1.Vout
