# Fritzing sketch id622_Temperature_Sensor_Sketch_0 (saved by Fritzing 0.9.2b)
breadboards: 2

parts:
  Part1 = Arduino Uno (Rev3)
  LED1 = smd LED [color="Red (633nm)" package="1206 [SMD]"]
  LED2 = smd LED [color="Green (555nm)" package="1206 [SMD]"]
  LED3 = smd LED [color="Yellow (595nm)" package="1206 [SMD]"]
  J1 = Piezo Speaker
  R1 = Resistor [tolerance=±5% resistance=220 package="0402 [SMD]"]
  R2 = Resistor [tolerance=±5% resistance=220 package="0402 [SMD]"]
  R3 = Resistor [tolerance=±5% resistance=220 package="0402 [SMD]"]
  T1 = LM35 Temperature Sensor [package="TO92 [THT]"]

nets:
  N1: Part1.A0, T1.Vout
  N2: Part1.D10_PWM/SS, J1.pin2
  N3: Part1.D11_PWM/MOSI, LED1.cathode, R1.Pin_0, R1.Pin_1
  N4: Part1.D12/MISO, LED3.cathode, R2.Pin_0, R2.Pin_1
  N5: Part1.D13/SCK, LED2.cathode, R3.Pin_0, R3.Pin_1
  GND: Part1.GND, LED1.anode, LED2.anode, LED3.anode, J1.pin1, T1.GND
  N6: Part1.5V, T1.+Vs
