# Fritzing sketch id624_Thermostat_0 (saved by Fritzing 0.7.11b)

parts:
  Arduino1 = Arduino Nano v3.0
  R1 = Resistor [tolerance=±5% resistance=680 package=THT]
  R2 = Resistor [tolerance=±5% resistance=1k package=THT]
  LED1 = LED - 5mm [color="Red (633nm)" package="5 mm [THT]"]
  R3 = Resistor [tolerance=±5% resistance=47 package=THT]
  U1 = Optocoupler [package=THT]
  R4 = Resistor [tolerance=±5% resistance=1k package=THT]
  Q1 = NPN-Transistor [part_number="TRIAC TIC206D" package="TO92 [THT]"]
  C1 = Ceramic Capacitor [capacitance=10nF package="100 mil [THT, multilayer]"]
  R5 = Resistor [tolerance=±5% resistance=47 package=THT]
  AC_in = Screw terminal - 2 pins [package=THT]
  to_heater = Screw terminal - 2 pins [package=THT]
  LED2 = LED - 5mm [color="Red (633nm)" package="5 mm [THT]"]
  R6 = Resistor [tolerance=±5% resistance=680 package=THT]
  R7 = Resistor [tolerance=±5% resistance=1k package=THT]
  U2 = TLP621 [package=THT]
  AC_in1 = Screw terminal - 2 pins [package=THT]
  to_heater1 = Screw terminal - 2 pins [package=THT]
  MAX31855 = IC, DIP package, 8 pins [chip_label=IC]
  U3 = mystery part, 2 pins [chip_label="K Thermocouple"]
  LCD1 = LCD screen
  R8 = Trimmer Potentiometer [maximum_resistance=10kΩ package=THT]
  J1 = male pin header, 3 pins [form="♂ (male)"]
  Set_Temp = Rotary Encoder [package=THT]

nets:
  TX: Arduino1.D1TX, J1.pin1
  RX: Arduino1.D0RX, J1.pin3
  GND: Arduino1.GND, LED1.cathode, U1.Pin_2, LED2.cathode, U2.Pin_2, MAX31855.pin1, LCD1.VSS, LCD1.R/W, LCD1.LED-, R8.leg1, J1.pin2
  SCK: Arduino1.D3, MAX31855.pin5
  SC: Arduino1.D4, MAX31855.pin6
  SO: Arduino1.D5, MAX31855.pin7
  RS: Arduino1.D7, LCD1.RS
  EN: Arduino1.D8, LCD1.E
  DB4: Arduino1.D9, LCD1.DB4
  DB5: Arduino1.D10, LCD1.DB5
  DB6: Arduino1.D11, LCD1.DB6
  DB7: Arduino1.D12, LCD1.DB7
  heater: Arduino1.D13, R1.Pin_0, R2.Pin_0, R6.Pin_0, R7.Pin_0
  3V3: Arduino1.3V3, MAX31855.pin4
  A: Arduino1.A0, Set_Temp.EncoderPinA
  C: Arduino1.A1, Set_Temp.EncoderPinC
  B: Arduino1.A2, Set_Temp.EncoderPinB
  5V: Arduino1.+5V, LCD1.VDD, LCD1.LED+, R8.leg2
  VCC: Arduino1.VIN
  N1: R1.Pin_1, LED1.anode
  N2: R2.Pin_1, U1.Pin_1
  N3: R3.Pin_0, U1.Pin_6
  N4: R3.Pin_1, Q1.C, R5.Pin_0, AC_in.pin1
  N5: U1.Pin_4, R4.Pin_0, Q1.B
  N6: R4.Pin_1, Q1.E, C1.0, to_heater.pin2
  N7: C1.1, R5.Pin_1
  N8: AC_in.pin2, to_heater.pin1
  N9: LED2.anode, R6.Pin_1
  N10: R7.Pin_1, U2.Pin_1
  N11: U2.Pin_4, AC_in1.pin1
  N12: U2.Pin_3, to_heater1.pin2
  N13: AC_in1.pin2, to_heater1.pin1
  TC+: MAX31855.pin2, U3.pin1
  TC-: MAX31855.pin3, U3.pin2
  N14: LCD1.V0, R8.wiper

notes:
  MOC3043
  xxxxx
  Solid State Relay
  http://learn.adafruit.com/character-lcds/wiring-a-character-lcd
  http://learn.adafruit.com/thermocouple/using-a-thermocouple
