# Fritzing sketch id625_file_0 (saved by Fritzing 0.8.3b)
breadboards: 1

parts:
  Componente1 = Arduino Uno (Rev3)
  R1 = Resistor [tolerance=±5% resistance=220 package=THT]
  LED1 = LED - 5mm [color="Infrared (940nm)" package="5 mm [THT]"]

nets:
  N1: Componente1.GND, R1.Pin_0
  N2: Componente1.D9_PWM, LED1.anode
  N3: R1.Pin_1, LED1.cathode
