# Fritzing sketch id627_i2C_128x32_Uno_0 (saved by Fritzing 0.9.0b)

parts:
  Part1 = Arduino Uno (Rev3)
  OLED1 = 128x32_I2C_Monochrome_OLED_Display

nets:
  N1: Part1.A4/SDA, OLED1.connector2
  N2: Part1.A5/SCL, OLED1.connector1
  N3: Part1.5V, OLED1.connector5
  N4: Part1.GND, OLED1.connector4
