# Fritzing sketch id628_DIY_Arduino_Traffic_Light_Pedestrian_Light_Push_Button_Control_0 (saved by Fritzing 0.9.2b)
breadboards: 1

parts:
  Part1 = Arduino Uno (Rev3)
  LED1 = LED - 5mm [color="Green (555nm)" package="5 mm [THT]"]
  LED2 = LED - 5mm [color="Yellow (595nm)" package="5 mm [THT]"]
  LED3 = LED - 5mm [color="Red (633nm)" package="5 mm [THT]"]
  LED4 = LED - 5mm [color="Red (633nm)" package="5 mm [THT]"]
  LED5 = LED - 5mm [color="Green (555nm)" package="5 mm [THT]"]
  R1 = Resistor [tolerance=±5% resistance=1k package=THT]
  R2 = Resistor [tolerance=±5% resistance=1k package=THT]
  R3 = Resistor [tolerance=±5% resistance=1k package=THT]
  R4 = Resistor [tolerance=±5% resistance=1k package=THT]
  R5 = Resistor [tolerance=±5% resistance=1k package=THT]
  S1 = Pushbutton [package="[THT]"]
  R6 = Resistor [tolerance=±5% resistance=1M package=THT]

nets:
  N1: Part1.D8, R4.Pin_1
  N2: Part1.D9_PWM, R5.Pin_1
  N3: LED1.cathode, LED2.cathode, LED3.cathode, LED4.cathode, LED5.cathode, R6.Pin_0
  N4: LED1.anode, R3.Pin_0
  N5: LED2.anode, R2.Pin_0
  N6: LED3.anode, R1.Pin_0
  N7: LED4.anode, R4.Pin_0
  N8: LED5.anode, R5.Pin_0
  N9: S1.Pin_1, S1.Pin_2
  N10: S1.Pin_3, S1.Pin_4, R6.Pin_1
