# Fritzing sketch id629_Arfuino_Traffic_Light_With_LED_Display_Timer_With_Push_Button_0 (saved by Fritzing 0.9.2b)
breadboards: 1

parts:
  Grove1 = Grove 4 Digit Display
  LED1 = LED - 5mm [color="Red (633nm)" package="5 mm [THT]"]
  LED2 = LED - 5mm [color="Yellow (592nm)" package="5 mm [THT]"]
  LED3 = LED - 5mm [color="Green (555nm)" package="5 mm [THT]"]
  R1 = Resistor [tolerance=±5% resistance=1k package=THT]
  Part1 = Arduino Uno (Rev3)
  S1 = Pushbutton [package="[THT]"]

nets:
  N1: Grove1.GND, LED1.cathode, LED3.cathode, R1.Pin_0
  VCC: Grove1.VCC, Part1.3V3
  N2: Grove1.DIO, Part1.D4
  N3: Grove1.CLK, Part1.D3_PWM
  N4: LED1.anode, Part1.D12/MISO
  N5: LED2.anode, Part1.D11_PWM/MOSI
  N6: LED3.anode, Part1.D13/SCK
  N7: R1.Pin_1, Part1.D1/TX, S1.Pin_1, S1.Pin_2
  N8: Part1.5V, S1.Pin_3, S1.Pin_4

notes:
  Guide by TheCustomizeWindows.COM
  Arduino Traffic Light With LED Display Timer With Push Button
