# Fritzing sketch id630_ARDUINO_SA_DVA_74HC595_0 (saved by Fritzing 0.8.3b)
breadboards: 1

parts:
  Arduino1 = Arduino
  U1 = 74HC595 [package="DIP16 [THT]"]
  U2 = 74HC595 [package="DIP16 [THT]"]
  LED1 = LED - 5mm [color="Red (633nm)" package="5 mm [THT]"]  # not connected
  LED2 = LED - 5mm [color="Red (633nm)" package="5 mm [THT]"]  # not connected
  LED3 = LED - 5mm [color="Red (633nm)" package="5 mm [THT]"]  # not connected
  LED4 = LED - 5mm [color="Red (633nm)" package="5 mm [THT]"]  # not connected
  LED5 = LED - 5mm [color="Red (633nm)" package="5 mm [THT]"]  # not connected
  LED6 = LED - 5mm [color="Red (633nm)" package="5 mm [THT]"]  # not connected
  LED7 = LED - 5mm [color="Red (633nm)" package="5 mm [THT]"]  # not connected
  LED8 = LED - 5mm [color="Red (633nm)" package="5 mm [THT]"]
  LED9 = LED - 5mm [color="Green (555nm)" package="5 mm [THT]"]  # not connected
  LED10 = LED - 5mm [color="Green (555nm)" package="5 mm [THT]"]  # not connected
  LED11 = LED - 5mm [color="Green (555nm)" package="5 mm [THT]"]  # not connected
  LED12 = LED - 5mm [color="Green (555nm)" package="5 mm [THT]"]  # not connected
  LED13 = LED - 5mm [color="Green (555nm)" package="5 mm [THT]"]  # not connected
  LED14 = LED - 5mm [color="Green (555nm)" package="5 mm [THT]"]  # not connected
  LED15 = LED - 5mm [color="Green (555nm)" package="5 mm [THT]"]  # not connected
  LED16 = LED - 5mm [color="Green (555nm)" package="5 mm [THT]"]
  R1 = Resistor [tolerance=±5% resistance=220 package=THT]
  R2 = Resistor [tolerance=±5% resistance=220 package=THT]
  R3 = Resistor [tolerance=±5% resistance=220 package=THT]
  R4 = Resistor [tolerance=±5% resistance=220 package=THT]
  R5 = Resistor [tolerance=±5% resistance=220 package=THT]
  R6 = Resistor [tolerance=±5% resistance=220 package=THT]
  R7 = Resistor [tolerance=±5% resistance=220 package=THT]
  R8 = Resistor [tolerance=±5% resistance=220 package=THT]
  R9 = Resistor [tolerance=±5% resistance=220 package=THT]
  R10 = Resistor [tolerance=±5% resistance=220 package=THT]
  R12 = Resistor [tolerance=±5% resistance=220 package=THT]
  R13 = Resistor [tolerance=±5% resistance=220 package=THT]
  R14 = Resistor [tolerance=±5% resistance=220 package=THT]
  R15 = Resistor [tolerance=±5% resistance=220 package=THT]
  R16 = Resistor [tolerance=±5% resistance=220 package=THT]
  R17 = Resistor [tolerance=±5% resistance=220 package=THT]
  U3 = atmega168 [package=dip]  # not connected

nets:
  N1: Arduino1.connector3, U1.SH_CP, U2.SH_CP
  N2: Arduino1.connector4, U1.DS
  N3: Arduino1.connector7, U1.MR
  VCC: Arduino1.connector18, U1.VCC, U2.MR, U2.VCC
  GND: Arduino1.connector20, U1.GND, U1.OE, U2.GND, U2.OE, LED8.cathode, LED16.cathode
  N4: U1.Q1, R2.Pin_1
  N5: U1.Q2, R3.Pin_1
  N6: U1.Q3, R4.Pin_1
  N7: U1.Q4, R5.Pin_1
  N8: U1.Q5, R6.Pin_1
  N9: U1.Q6, R7.Pin_1
  N10: U1.Q7, R8.Pin_1
  N11: U1.Q7', U2.DS
  N12: U1.Q0, R1.Pin_1
  N13: U2.Q1, R10.Pin_1
  N14: U2.Q2, R17.Pin_1
  N15: U2.Q3, R12.Pin_1
  N16: U2.Q4, R13.Pin_1
  N17: U2.Q5, R14.Pin_1
  N18: U2.Q6, R15.Pin_1
  N19: U2.Q7, R16.Pin_1
  N20: U2.Q0, R9.Pin_1
