# Fritzing sketch id631_Untitled_Sketch_2_0 (saved by Fritzing 0.8.3b)

parts:
  U1 = generic_sip_4_300mil.fzp [chip_label=IC]
  Componente1 = Arduino Uno (Rev3)

nets:
  N1: U1.connector0, Componente1.3V3
  N2: U1.connector1, Componente1.D2
  N3: U1.connector2, Componente1.D4
  N4: U1.connector3, Componente1.GND
