# Fritzing sketch id633_ArduinoUNO_and_7_Segment_display_simple_circuit_0 (saved by Fritzing 0.9.3b)
breadboards: 1

parts:
  Bauteil1 = Arduino Uno (Rev3)
  U1 = 7-SEGMENT-DISPLAY [package=7-segment-display]
  R8 = Resistor [tolerance=±5% resistance=220 package=THT]

nets:
  N1: Bauteil1.D8, U1.E
  N2: Bauteil1.D9_PWM, U1.B
  N3: Bauteil1.D2, U1.G2
  N4: Bauteil1.D3_PWM, U1.A
  N5: Bauteil1.D4, U1.DP
  N6: Bauteil1.D5_PWM, U1.G1
  N7: Bauteil1.D6_PWM, U1.D
  N8: Bauteil1.D7, U1.G
  N9: Bauteil1.GND, R8.Pin_0
  N10: U1.C, U1.F, R8.Pin_1

notes:
  Only the common cathode need a resistor (220Ohm or 330Ohm). All anodes dont's needs a resistor (parallel connection)!
  So it's simple to wiring directly with the Arduino UNO! :-)
  You can find all parts in the ArdDevKIT1 from ALLNET (allnet.de, reichelt.de, conrad.de) or other electronic dealers.
  The 7-segment display is a sparkfun-led-segment-display with common cathode.
