# Fritzing sketch id634_Demo_Board_018_0 (saved by Fritzing 0.9.3b)
circuit board: 6.88566cm x 5.36311cm
breadboards: 1

parts:
  Part1 = Arduino Uno (Rev3)
  D13 = LED - 5mm [color="Red (633nm)" package="5 mm [THT]"]
  D12 = LED - 5mm [color="Red (633nm)" package="5 mm [THT]"]
  D11~ = LED - 5mm [color="Red (633nm)" package="5 mm [THT]"]
  D10~ = LED - 5mm [color="Red (633nm)" package="5 mm [THT]"]
  D9~ = LED - 5mm [color="Red (633nm)" package="5 mm [THT]"]
  D8 = LED - 5mm [color="Red (633nm)" package="5 mm [THT]"]
  D7 = LED - 5mm [color="Red (633nm)" package="5 mm [THT]"]
  220R = Resistor [tolerance=±5% resistance=220 package=THT]
  220R_2 = Resistor [tolerance=±5% resistance=220 package=THT]
  220R_3 = Resistor [tolerance=±5% resistance=220 package=THT]
  SW(D2) = Pushbutton [package=THT]
  220R_4 = Resistor [tolerance=±5% resistance=220 package=THT]
  220R_5 = Resistor [tolerance=±5% resistance=220 package=THT]
  220R_6 = Resistor [tolerance=±5% resistance=220 package=THT]
  220R_7 = Resistor [tolerance=±5% resistance=220 package=THT]
  Pot_(A5) = Rotary Potentiometer (Small) [maximum_resistance=10kΩ package=THT]
  10KR = Resistor [tolerance=±5% resistance=10k package=THT]
  Reset = Momentary Switch [package=ksa_sealed_tac_switch]
  LDR(A0) = PHOTOCELL [package=photocell-kit]
  Power = LED - 3mm [color="Red (633nm)" package="3 mm [THT]"]
  560R = Resistor [tolerance=±5% resistance=220 package=THT]
  Buzzer_(D6~) = Buzzer 12mm [package=buzzer-12mm-ns]
  10KR_2 = Resistor [tolerance=±5% resistance=220 package=THT]
  J1 = female pin header, 10 pins [form="♀ (female)"]
  J3 = female pin header, 8 pins [form="♀ (female)"]
  J4 = female pin header, 8 pins [form="♀ (female)"]
  J7 = female pin header, 3 pins [form="♀ (female)"]  # not connected
  J6 = female pin header, 3 pins [form="♀ (female)"]  # not connected
  J5 = female pin header, 3 pins [form="♀ (female)"]  # not connected
  J10 = female pin header, 12 pins [form="♀ (female)"]  # not connected
  J11 = female pin header, 12 pins [form="♀ (female)"]  # not connected
  J12 = female pin header, 12 pins [form="♀ (female)"]  # not connected
  J8 = female pin header, 3 pins [form="♀ (female)"]  # not connected

nets:
  N1: Part1.A0, LDR(A0).P$2, 10KR_2.Pin_0
  N2: Part1.A4/SDA, J1.pin9
  N3: Part1.A5/SCL, Pot_(A5).wiper, J1.pin10
  N4: Part1.D8, D8.anode, J1.pin1
  N5: Part1.D9_PWM, D9~.anode, J1.pin2
  N6: Part1.D10_PWM/SS, D10~.anode, J1.pin3
  N7: Part1.D11_PWM/MOSI, D11~.anode, J1.pin4
  N8: Part1.D12/MISO, D12.anode, J1.pin5
  N9: Part1.D13/SCK, D13.anode, J1.pin6
  N10: Part1.GND, 220R.Pin_0, 220R_2.Pin_0, 220R_3.Pin_0, 220R_4.Pin_0, 220R_5.Pin_0, 220R_6.Pin_0, 220R_7.Pin_0, Pot_(A5).leg2, 10KR.Pin_1, Reset.3, Power.cathode, Buzzer_(D6~).2, 10KR_2.Pin_1, J1.pin7, J3.pin2, J3.pin3
  N11: Part1.AREF, J1.pin8
  N12: Part1.D0/RX, J4.pin1
  N13: Part1.D1/TX, J4.pin2
  N14: Part1.D2, SW(D2).leg0, 10KR.Pin_0, J4.pin3
  N15: Part1.D3_PWM, J4.pin4
  N16: Part1.D4, J4.pin5
  N17: Part1.D5_PWM, J4.pin6
  N18: Part1.D6_PWM, Buzzer_(D6~).1, J4.pin7
  N19: Part1.D7, D7.anode, J4.pin8
  N20: Part1.ioref, J3.pin7
  N21: Part1.RESET, Reset.4, J3.pin6
  N22: Part1.3V3, J3.pin5
  N23: Part1.5V, SW(D2).leg1, Pot_(A5).leg1, LDR(A0).P$1, 560R.Pin_1, J3.pin4
  N24: Part1.VIN, J3.pin1
  N25: Part1.N/C, J3.pin8
  N26: D13.cathode, 220R_2.Pin_1
  N27: D12.cathode, 220R.Pin_1
  N28: D11~.cathode, 220R_3.Pin_1
  N29: D10~.cathode, 220R_4.Pin_1
  N30: D9~.cathode, 220R_5.Pin_1
  N31: D8.cathode, 220R_6.Pin_1
  N32: D7.cathode, 220R_7.Pin_1
  N33: Power.anode, 560R.Pin_0
