# Fritzing sketch id635_Arduino_Uno_ethernet_shield_webserver_e_relay_0 (saved by Fritzing 0.9.3b)

parts:
  Componente1 = Arduino Uno (Rev3)  # not connected
  Componente2 = Arduino Ethernet Shield (Rev3)
  KY-1 = keyes
  KY-2 = keyes
  KY-3 = keyes
  KY-4 = keyes

nets:
  N1: Componente2.D2, KY-4.connector0
  N2: Componente2.PWM_D3, KY-3.connector0
  N3: Componente2.SDCS, KY-2.connector0
  N4: Componente2.PWM_D5, KY-1.connector0
  N5: Componente2.5V, KY-4.connector1
