# Fritzing sketch id637_Arduino_Uno_With_LCD_0 (saved by Fritzing 0.9.3b)
breadboards: 1

parts:
  Part1 = Arduino Uno (Rev3)
  LCD1 = LCD screen
  R1 = Rotary Potentiometer (Small) [maximum_resistance=100kΩ package=THT]

nets:
  N1: Part1.D8, LCD1.E
  N2: Part1.D9_PWM, LCD1.DB4
  N3: Part1.D10_PWM/SS, LCD1.DB5
  N4: Part1.D11_PWM/MOSI, LCD1.DB6
  N5: Part1.D12/MISO, LCD1.DB7
  N6: Part1.D7, LCD1.RS
  5V: Part1.5V, LCD1.VDD, LCD1.R/W, LCD1.LED+, LCD1.LED-, R1.leg1
  GND: Part1.GND, LCD1.VSS, R1.leg2
  N7: LCD1.V0, R1.wiper
