# Fritzing sketch id638_PIR_Arduino_0 (saved by Fritzing 0.9.3b)
breadboards: 1

parts:
  PIR1 = PIR_sensor
  Part1 = Arduino Uno (Rev3) - ICSP
  LED2 = LED - 5mm [color="Red (633nm)" package="5 mm [THT]"]
  J1 = Piezo Speaker
  R1 = Resistor [tolerance=±5% resistance=220 package="0805 [SMD]"]

nets:
  N1: PIR1.connector1, Part1.5V
  N2: PIR1.connector2, Part1.D2
  N3: PIR1.connector3, Part1.GND, LED2.cathode, J1.pin1
  N4: Part1.D3_PWM, J1.pin2, R1.Pin_0
  N5: LED2.anode, R1.Pin_1
