# Fritzing sketch id639_Arduino_Joystick_Receiver_0 (saved by Fritzing 0.9.0b)

parts:
  NRF24L1 = NRF24L01
  Componente1 = Arduino Uno (Rev3) - ICSP

nets:
  N1: NRF24L1.connector0, Componente1.3V3
  N2: NRF24L1.connector1, Componente1.D10_PWM/SS
  N3: NRF24L1.connector2, Componente1.ICSP_MOSI, Componente1.D11_PWM/MOSI
  N4: NRF24L1.connector4, Componente1.GND
  N5: NRF24L1.connector5, Componente1.D9_PWM
  N6: NRF24L1.connector6, Componente1.D13/SCK
  N7: NRF24L1.connector7, Componente1.ICSP_MISO, Componente1.D12/MISO

notes:
  GND = Black
  VCC = Red
  CE = Yellow
  CSN = Green
  SCK = Orange
  MOSI = White
  MISO = Brown
  IRQ = Not Connected
  This connection are intended looking the TOP of the NRF24L01(as image suggested)
  if you "t u r n" the NRF24L01 upsidedown , take care to not invert some wire
