# Fritzing sketch id641_servo_with_led_indication_and_lcd_display_0 (saved by Fritzing 0.8.3b)
breadboards: 1

parts:
  Part1 = Arduino Uno (Rev3)
  LCD1 = LCD screen
  R1 = Trimmer Potentiometer [maximum_resistance=10kΩ package=THT]  # not connected
  LED1 = LED - 5mm [color="Red (633nm)" package="5 mm [THT]"]
  LED2 = LED - 5mm [color="Green (555nm)" package="5 mm [THT]"]
  R2 = Resistor [tolerance=±5% resistance=220 package=THT]
  R3 = Resistor [tolerance=±5% resistance=220 package=THT]
  J1 = Basic Servo

nets:
  N1: Part1.D9_PWM, J1.pulse
  N2: Part1.D11_PWM/MOSI, LCD1.E
  N3: Part1.D12/MISO, LCD1.RS
  GND: Part1.GND, LCD1.VSS, LCD1.R/W, LED1.cathode, LED2.cathode, J1.gnd
  N4: Part1.D2, LCD1.DB7
  N5: Part1.D3_PWM, LCD1.DB6
  N6: Part1.D4, LCD1.DB5
  N7: Part1.D5_PWM, LCD1.DB4
  N8: Part1.D7, R3.Pin_0
  5V: Part1.5V, LCD1.VDD, J1.vcc
  N9: LED1.anode, R2.Pin_1
  N10: LED2.anode, R3.Pin_1
