# Fritzing sketch id642_Uno_RGB_Sketch_0 (saved by Fritzing 0.9.2b)
breadboards: 1

parts:
  Eleman1 = Arduino Uno (Rev3)
  LED1 = RGB LED (com. cathode, rbg) [package="5 mm [THT]"]
  R1 = Resistor [tolerance=±5% resistance=220 package=THT]

nets:
  N1: Eleman1.D9_PWM, LED1.red_anode
  N2: Eleman1.D10_PWM/SS, LED1.blue_anode
  N3: Eleman1.D11_PWM/MOSI, LED1.green_anode
  N4: Eleman1.5V, R1.Pin_1
  N5: LED1.common_cathode, R1.Pin_0
