# Fritzing sketch id643_Arduino_Uhr_0 (saved by Fritzing 0.9.2b)
breadboards: 1

parts:
  Bauteil1 = Arduino Uno (Rev3)
  J1 = Piezo Speaker
  Bauteil2 = Real Time Clock Module - DS1307 RTC Breakout Board
  Grove1 = Grove OLED 128x96
  R1 = Temperature Sensor (Thermistor) [thermistor_type=NTC package=THT]
  10k_Ohm_Widerstand! = Resistor [tolerance=±5% resistance=220 package="0805 [SMD]"]

nets:
  N1: Bauteil1.A0, R1.pin_0, 10k_Ohm_Widerstand!.Pin_1
  N2: Bauteil1.A4/SDA, Bauteil2.SDA, Grove1.SDA
  N3: Bauteil1.A5/SCL, Bauteil2.SCL, Grove1.SCL
  N4: Bauteil1.D9_PWM, J1.pin2
  GND: Bauteil1.GND, J1.pin1, Bauteil2.GND, Grove1.GND, 10k_Ohm_Widerstand!.Pin_0
  5V: Bauteil1.5V, Bauteil2.5V, Grove1.VCC, R1.pin_1
