# Fritzing sketch id644_night_lamp_0 (saved by Fritzing 0.9.2b)
breadboards: 1

parts:
  Part1 = Arduino Uno (Rev3)
  R1 = Resistor [tolerance=±5% resistance=220 package=THT]
  R2 = Photocell (LDR) [package=THT]  # not connected
  R3 = Resistor [tolerance=±5% resistance=1k package=THT]
  LED1 = LED - 5mm [color="Red (633nm)" package="5 mm [THT]"]

nets:
  N1: Part1.A0, R3.Pin_0
  N2: Part1.D8, R1.Pin_1
  N3: Part1.GND, R3.Pin_1, LED1.anode
