# Fritzing sketch id645_4N35_Soft_Reset_0 (saved by Fritzing 0.9.3b)
breadboards: 1

parts:
  IC1 = IC, DIP package, 6 pins [chip_label=4N35]
  R1 = Resistor [tolerance=±5% resistance=220 package=THT]
  R2 = Rotary Potentiometer (Small) [maximum_resistance=10kΩ package=THT]
  Genuino/Arduino_UNO = Arduino Uno (Rev3)

nets:
  N1: IC1.pin1, R1.Pin_1
  GND: IC1.pin2, IC1.pin4, R2.leg1, Genuino/Arduino_UNO.GND
  N2: IC1.pin5, Genuino/Arduino_UNO.RESET
  N3: R1.Pin_0, Genuino/Arduino_UNO.D3_PWM
  N4: R2.wiper, Genuino/Arduino_UNO.A0
  N5: R2.leg2, Genuino/Arduino_UNO.5V
