# Fritzing sketch id646_ArduinoUNO_and_esp8266_weather_station_0 (saved by Fritzing 0.9.3b)

parts:
  U1 = ESP8266_module [part_number=ESP8266]
  Part1 = Arduino Uno (Rev3)
  R1 = Resistor [tolerance=±5% resistance=10k package=THT]
  R2 = Resistor [tolerance=±5% resistance=10k package=THT]
  S1 = SWITCH-MOMENTARY-2 [package=tactile_switch_tall]  # not connected
  RHT1 = Humidity and Temperature Sensor RHT03 [part_number=dht22]
  MQ3 = female pin header, 4 pins [form="♀ (female)"]
  R3 = Photocell (LDR) [package=THT]
  R4 = Resistor [tolerance=±5% resistance=1k package=THT]
  LCD2 = LCD screen
  LCM1602_IIC3 = generic_ic_dip_22_300mil.fzp [part_number="LCM1602 IIC" chip_label="LCM1602 IIC"]

nets:
  N1: U1.connector0, Part1.D11_PWM/MOSI
  N2: U1.connector3, R2.Pin_0
  N3: U1.connector5, R1.Pin_0
  N4: U1.connector6, Part1.GND, RHT1.GND_2
  N5: U1.connector7, Part1.D10_PWM/SS
  N6: Part1.A0, MQ3.pin1
  N7: Part1.A4/SDA, LCM1602_IIC3.connector17, LCM1602_IIC3.connector18
  N8: Part1.A5/SCL, LCM1602_IIC3.connector19
  N9: Part1.D12/MISO, RHT1.Data-signal
  N10: Part1.3V3, R1.Pin_1
  N11: R3.pin_1, R4.Pin_1
  N12: LCD2.VSS, LCM1602_IIC3.connector0
  N13: LCD2.VDD, LCM1602_IIC3.connector1
  N14: LCD2.V0, LCM1602_IIC3.connector2
  N15: LCD2.RS, LCM1602_IIC3.connector3
  N16: LCD2.R/W, LCM1602_IIC3.connector4
  N17: LCD2.E, LCM1602_IIC3.connector5
  N18: LCD2.DB0, LCM1602_IIC3.connector6
  N19: LCD2.DB1, LCM1602_IIC3.connector7
  N20: LCD2.DB2, LCM1602_IIC3.connector8
  N21: LCD2.DB3, LCM1602_IIC3.connector9
  N22: LCD2.DB4, LCM1602_IIC3.connector10
  N23: LCD2.DB5, LCM1602_IIC3.connector11
  N24: LCD2.DB6, LCM1602_IIC3.connector12
  N25: LCD2.DB7, LCM1602_IIC3.connector13
  N26: LCD2.LED+, LCM1602_IIC3.connector14
  N27: LCD2.LED-, LCM1602_IIC3.connector15
  N28: LCM1602_IIC3.connector20, LCM1602_IIC3.connector21
