# Fritzing sketch id647_GiornoVirtualev2_0 (saved by Fritzing 0.8.7b)
breadboards: 1

parts:
  S1 = Pushbutton [package="[THT]"]
  S2 = Pushbutton [package="[THT]"]
  S3 = Pushbutton [package="[THT]"]
  J1 = Screw terminal - 2 pins [package=THT]
  U1 = Voltage Regulator - 5V [package="TO220 [THT]"]
  Q1 = Basic FET N-Channel [package="TO220 [THT]"]
  R1 = Resistor [tolerance=±5% resistance=330 package=THT]
  R2 = Resistor [tolerance=±5% resistance=330 package=THT]
  R3 = Resistor [tolerance=±5% resistance=330 package=THT]
  J2 = Screw terminal - 2 pins [package=THT]
  C1 = Electrolytic Capacitor [capacitance=1µF package="100 mil [THT, electrolytic]"]
  C2 = Ceramic Capacitor [capacitance=100nF package="100 mil [THT, multilayer]"]
  C3 = Ceramic Capacitor [capacitance=100nF package="100 mil [THT, multilayer]"]
  LCD1 = LCD screen
  R4 = Resistor [tolerance=±5% resistance=330 package=THT]
  part = Resistor [tolerance=±5% resistance=220 package=THT]  # not connected
  Arduino1 = Arduino Mini (Rev5)

nets:
  N1: S1.Pin_1, S1.Pin_2, S2.Pin_1, S2.Pin_2, S3.Pin_3, S3.Pin_4, R3.Pin_0, Arduino1.A0
  N2: S1.Pin_3, S1.Pin_4, R1.Pin_0, R4.Pin_1
  N3: S2.Pin_3, S2.Pin_4, R1.Pin_1, R2.Pin_0
  N4: S3.Pin_1, S3.Pin_2, R2.Pin_1
  GND: J1.pin1, U1.GND, R3.Pin_1, J2.pin2, C1.-, C2.1, C3.1, LCD1.VSS, Arduino1.GND
  N5: J1.pin2, U1.input_voltage, Q1.drain, C2.0
  VDD: U1.output_voltage, C3.0, LCD1.VDD, R4.Pin_0, Arduino1.5V
  N6: Q1.gate, Arduino1.D11_PWM
  N7: Q1.source, J2.pin1
  N8: LCD1.RS, LCD1.R/W, Arduino1.D2
  N9: LCD1.E, LCD1.DB0, Arduino1.D3_PWM
  N10: LCD1.DB3, LCD1.DB4, Arduino1.D7
  N11: LCD1.DB5, Arduino1.D4
  N12: LCD1.DB6, Arduino1.D6_PWM
  N13: LCD1.DB7, LCD1.LED+, Arduino1.D5_PWM

notes:
  IN 12V
  12V alla barra LED
  MOSFET N
  10uF
  A0
  D11
  7805
  2 x 10uF
