# Fritzing sketch id648_Arduino_VoiceRecognition_0 (saved by Fritzing 0.8.7b)
breadboards: 1

parts:
  Componente1 = Arduino Uno (Rev3) - ICSP  # not connected
  U1 = XBee
  T1 = DS18B20_Temperature_Sensor [part_number=DS18B20]
  R1 = Resistor [tolerance=±5% resistance=4.7k package=THT]
  R2 = PHOTOCELL [package=photocell]
  R3 = Resistor [tolerance=±5% resistance=10k package=THT]

nets:
  N1: U1.connector9, T1.connector0, R2.P$1
  N2: T1.connector1, R1.Pin_0
  N3: T1.connector2, R1.Pin_1, R3.Pin_1
  N4: R2.P$2, R3.Pin_0

notes:
  EASYVR Shild
  need to be mounted on an Arduino
  DS18B20
  Resistor pull-up 4.7 K
  Photoresistor
  Resistor pull-up 10 K
