# Fritzing sketch id649_divisor_tension_arduino_acarduino_0 (saved by Fritzing 0.9.2b)
circuit board: 8.46667cm x 5.64444cm
breadboards: 1

parts:
  R1 = Resistor [tolerance=±5% resistance=220 package=THT]
  R2 = Resistor [tolerance=±5% resistance=220 package=THT]
  R3 = Resistor [tolerance=±5% resistance=220 package=THT]
  Parte1 = Arduino Uno (Rev3)
  VCC1 = prefix0001

nets:
  N1: R1.Pin_0, Parte1.VIN, VCC1.connector1
  N2: R1.Pin_1, R2.Pin_0
  N3: R2.Pin_1, R3.Pin_0, Parte1.A0
  N4: R3.Pin_1, Parte1.GND, VCC1.connector0
