# Fritzing sketch id650_Arduino_voltage_and_current_0 (saved by Fritzing 0.9.3b)

parts:
  Part1 = Arduino Nano (Rev3.0)
  Part2 = adafruit [part_number="Adafruit #1083"]
  R7 = Resistor [tolerance=±5% resistance=4.7k package="0402 [SMD]"]
  R8 = Resistor [tolerance=±5% resistance=47k package="0402 [SMD]"]
  Part3 = ACS712 Low Current Sensor Board v12
  R9 = Resistor [tolerance=±5% resistance=2 package=THT]
  V1 = DC Power [voltage=15]
  V2 = DC Power [voltage=5]

nets (from the schematic view):
  N1: Part1.GND, Part2.connector15, V2.V-
  5V: Part1.5V, Part2.connector11, Part2.connector19, Part3.5V, V2.V+
  N2: Part1.A5, Part2.connector17
  N3: Part1.A4, Part2.connector16
  N4: Part2.connector12, Part3.VO
  N5: Part2.connector13, R7.Pin_1, R8.Pin_0
  N6: R7.Pin_0, Part3.IP-, Part3.GND, V1.V-
  N7: R8.Pin_1, R9.Pin_1, V1.V+
  N8: Part3.IP+, R9.Pin_0
