# Fritzing sketch id651_Arduino_voltometro_voltmetro_voltmeter_0 (saved by Fritzing 0.9.2b)
breadboards: 1

parts:
  Componente1 = Arduino Uno (Rev3)
  R2_10k = Resistor [tolerance=±1% resistance=10k package=THT]
  R1_100k = Resistor [tolerance=±1% resistance=100k package=THT]
  BAT1 = BC9VPC [package=bc9vpc]
  LCD1 = LCD screen  # not connected

nets:
  N1: Componente1.A0, R2_10k.Pin_1, R1_100k.Pin_1
  N2: Componente1.GND, R2_10k.Pin_0, BAT1.V-
  N3: R1_100k.Pin_0, BAT1.V+

notes:
  DC VOLT INPUT
  SCL
  SDA
