# Fritzing sketch id652_VU_Meter_0 (saved by Fritzing 0.8.7b)
breadboards: 1

parts:
  R1 = Resistor [tolerance=±5% resistance=120 package=THT]
  R2 = Resistor [tolerance=±5% resistance=120 package=THT]
  R3 = Resistor [tolerance=±5% resistance=120 package=THT]
  R4 = Resistor [tolerance=±5% resistance=120 package=THT]
  R5 = Resistor [tolerance=±5% resistance=120 package=THT]
  R6 = Resistor [tolerance=±5% resistance=120 package=THT]
  R7 = Resistor [tolerance=±5% resistance=120 package=THT]
  R8 = Resistor [tolerance=±5% resistance=120 package=THT]
  R9 = Resistor [tolerance=±5% resistance=120 package=THT]
  R10 = Resistor [tolerance=±5% resistance=120 package=THT]
  TRS1 = Audio Jack (TRS) 3.5mm [package="PG203J [THT]"]
  Componente1 = Arduino Uno (Rev3)
  LED1 = LED - 5mm [color="Red (633nm)" package="5 mm [THT]"]
  LED2 = LED - 5mm [color="Red (633nm)" package="5 mm [THT]"]
  LED3 = LED - 5mm [color="Yellow (595nm)" package="5 mm [THT]"]
  LED4 = LED - 5mm [color="Yellow (595nm)" package="5 mm [THT]"]
  LED5 = LED - 5mm [color="Yellow (595nm)" package="5 mm [THT]"]
  LED6 = LED - 5mm [color="Green (570nm)" package="5 mm [THT]"]
  LED7 = LED - 5mm [color="Green (570nm)" package="5 mm [THT]"]
  LED8 = LED - 5mm [color="Green (570nm)" package="5 mm [THT]"]
  LED9 = LED - 5mm [color="Green (570nm)" package="5 mm [THT]"]
  LED10 = LED - 5mm [color="Green (570nm)" package="5 mm [THT]"]

nets:
  N1: R1.Pin_0, Componente1.D10_PWM/SS
  N2: R1.Pin_1, LED1.cathode
  N3: R2.Pin_0, Componente1.D9_PWM
  N4: R2.Pin_1, LED2.cathode
  N5: R3.Pin_0, Componente1.D8
  N6: R3.Pin_1, LED3.cathode
  N7: R4.Pin_0, Componente1.D7
  N8: R4.Pin_1, LED4.cathode
  N9: R5.Pin_0, Componente1.D6_PWM
  N10: R5.Pin_1, LED5.cathode
  N11: R6.Pin_0, Componente1.D5_PWM
  N12: R6.Pin_1, LED6.cathode
  N13: R7.Pin_0, Componente1.D4
  N14: R7.Pin_1, LED7.cathode
  N15: R8.Pin_0, Componente1.D3_PWM
  N16: R8.Pin_1, LED8.cathode
  N17: R9.Pin_0, Componente1.D2
  N18: R9.Pin_1, LED9.cathode
  N19: R10.Pin_0, Componente1.D1/TX
  N20: R10.Pin_1, LED10.cathode
  N21: TRS1.Sleeve, Componente1.GND, LED1.anode, LED2.anode, LED3.anode, LED4.anode, LED5.anode, LED6.anode, LED7.anode, LED8.anode, LED9.anode, LED10.anode
  N22: TRS1.Ring, Componente1.A0

notes:
  /*
  * Arduino VU-Meter v1.0
  * Developed by Cesário Garcia Mil-Homens
  * http://www.hypatia.pt - Formação e consultoria, Lda.
  *
  */
  int o; // Output
  int a; // Turn LED on
  int b; // Turn LED off
  void setup() {
  Serial.begin(9600); // Configuration for monitoring the signal, removing the review to check the values​​
  for (o=1; o<=10; o++) { // Setting pins 0 to 10 as 5V outputs, through a for loop
  pinMode(o, OUTPUT);
  }
  }
  void loop() {
  int audio = analogRead(0); // Reading the analog pin 0
  //Serial.println(audio); // Print the serial monitor the value of the measurement performed on pin 0
  //delay(100); // 100ms delay to view measured signal on pin 0
  audio = audio / 25; // Dividing by 25 is possible to obtain values ​​1-10 for the new value of audio
  //Serial.println(audio); // Print to serial monitor the value 1 to 10
  //delay(100); // 100ms delay to view signal in serial monitor from 1 to 10
  for (a=1; a<=audio; ++a) { // Turn ON LED
  digitalWrite(a, HIGH);
  }
  for (b=10; b>audio; --b) { // Turn OFF LED
  digitalWrite(b, LOW);
  }
  for (a=1; a<=10; ++a) { // Reset LED
  digitalWrite(a, LOW);
  }
  }
