# Fritzing sketch id653_Arduino_Weather_Logger_0 (saved by Fritzing 0.9.2b)
breadboards: 1

parts:
  Pressure_and_Temperature_Sensor = Barometric Pressure Sensor - BMP180 Breakout (GY-68)
  Part2 = Arduino Nano (Rev3.0)
  Light_Sensor = Photocell (LDR) [package=THT]
  R2 = Resistor [tolerance=±5% resistance=100k package="2512 [SMD]"]
  R2_2 = Resistor [tolerance=±5% resistance=100k package="2010 [SMD]"]
  Wifi = ESP8266_module [part_number=ESP8266]

nets:
  VCC: Pressure_and_Temperature_Sensor.VCC, Part2.3V3
  GND: Pressure_and_Temperature_Sensor.GND, Part2.GND, R2.Pin_1, R2_2.Pin_1, Wifi.connector6
  N1: Pressure_and_Temperature_Sensor.SCL, Part2.A5
  N2: Pressure_and_Temperature_Sensor.SDA, Part2.A4
  N3: Part2.D1/TX, Wifi.connector0
  N4: Part2.D0/RX, Wifi.connector7
  N5: Part2.5V, Light_Sensor.pin_0, Wifi.connector1, Wifi.connector5
  N6: Part2.A0, Light_Sensor.pin_1, R2.Pin_0, R2_2.Pin_0
