# Fritzing sketch id655_UDMOProyectoArduino_0 (saved by Fritzing 0.9.1b)
breadboards: 1

parts:
  Parte1 = Arduino Uno (Rev3)  # not connected
  JP1 = Header 2 [package=jst-2-pth-ns]
  JP2 = Header 2 [package=jst-2-pth-ns]
  JP3 = Header 2 [package=jst-2-pth-ns]
  JP4 = Header 2 [package=jst-2-pth-ns]
  Parte2 = Arduino Ethernet Shield (Rev3)
  R1 = Resistor [tolerance=±5% resistance=330 package="1206 [SMD]"]
  R2 = Resistor [tolerance=±5% resistance=330 package="1206 [SMD]"]
  LED1 = RGB LED (com. cathode, rbg) [package="5 mm [THT]"]
  J1 = Piezo Speaker
  J2 = Basic Servo
  R3 = Basic Flex Resistor
  R4 = Resistor [tolerance=±5% resistance=10k package="1206 [SMD]"]
  R5 = Resistor [tolerance=±5% resistance=10k package="1206 [SMD]"]
  R6 = PHOTOCELL [package=photocell-kit]
  U1 = TMP36 [package=to-92-kit]
  U2 = POT [package=pot_mammoth]

nets:
  VCC: JP1.1, JP3.1, Parte2.5V, J2.vcc, R3.pin_1, R5.Pin_1, U1.VCC, U2.S
  GND: JP1.2, JP3.2, Parte2.GND, LED1.common_cathode, J1.pin1, J2.gnd, R4.Pin_0, R6.P$2, U1.GND, U2.E
  N1: JP2.1, JP4.1
  N2: JP2.2, JP4.2
  N3: Parte2.PWM_D9, R1.Pin_0
  N4: Parte2.A0, R5.Pin_0, R6.P$1
  N5: Parte2.A1, U1.VOUT
  N6: Parte2.A3, U2.A
  N7: Parte2.A4/SDA, R3.Pin_2, R4.Pin_1
  N8: Parte2.A5/SCL, J2.pulse
  N9: Parte2.PWM_D3, R2.Pin_0
  N10: Parte2.PWM_D5, J1.pin2
  N11: R1.Pin_1, LED1.red_anode
  N12: R2.Pin_1, LED1.green_anode

notes:
  Fancy Sensing
  Soft Potentiometer
  Micro Servo
  9g A0090
  CET12A3.5
  12 +135
  Pin Header x2(idem en los demas)
  Wifi Shield(no hay libreria en Fritzing)
  El ETH CS es el ~10
