# Fritzing sketch id657_Bluetooth_HC_05_0 (saved by Fritzing 0.9.2b)
breadboards: 1

parts:
  Componente1 = Arduino Uno (Rev3)
  Part2 = Bluetooth HC-05 Macho
  R1 = Resistor [tolerance=±5% resistance=10k package=THT]
  R2 = Resistor [tolerance=±5% resistance=20k package=THT]

nets:
  GND: Componente1.GND, Part2.GND, R2.Pin_1
  N1: Componente1.D2, Part2.TXD
  N2: Componente1.D3_PWM, R1.Pin_0
  N3: Componente1.3V3, Part2.Key
  5V: Componente1.5V, Part2.VCC
  N4: Part2.RXD, R1.Pin_1, R2.Pin_0
