# Fritzing sketch id658_Arduino_with_HC_05_0 (saved by Fritzing 0.9.3b)

parts:
  元件1 = Arduino Uno (Rev3)
  元件2 = Bluetooth HC-05 Macho

nets:
  N1: 元件1.D8, 元件2.RXD
  N2: 元件1.D7, 元件2.TXD
  N3: 元件1.3V3, 元件2.Key
  5V: 元件1.5V, 元件2.VCC
  GND: 元件1.GND, 元件2.GND

notes:
  The circuit:
  * RX is digital pin 7 (connect to TX of other device)
  * TX is digital pin 8 (connect to RX of other device)
