# Fritzing sketch id659_display1602_arduino_1_and_irRemote_0 (saved by Fritzing 0.9.2b)
breadboards: 1

parts:
  LCD1 = LCD screen
  Componente1 = Arduino Uno (Rev3)
  U1 = POT [package=3362u]
  IR1 = TSOP312.., 314.. [package=THT]
  R1 = Resistor [tolerance=±5% resistance=330 package="0402 [SMD]"]

nets:
  GND: LCD1.VSS, LCD1.R/W, Componente1.GND, U1.E, IR1.GND, R1.Pin_1
  VDD: LCD1.VDD, Componente1.5V, U1.A, IR1.Vs, R1.Pin_0
  N1: LCD1.V0, U1.S
  N2: LCD1.RS, Componente1.D2
  N3: LCD1.E, Componente1.D3_PWM
  N4: LCD1.DB4, Componente1.D4
  N5: LCD1.DB5, Componente1.D5_PWM
  N6: LCD1.DB6, Componente1.D6_PWM
  N7: LCD1.DB7, Componente1.D7
  N8: Componente1.D8, IR1.Data

notes:
  I pin led, si possono collegare ad un trimmer per regolare la luminosità
  Io ho usato un ricevitore ir tipo:
  tsop4838 dip-3 recuperato che non è quello dello sketc.
  Questo sketc è spudoratamente copiato da vari siti (www.brescianet.com) e libri e deve servire come base di partenza per sviluppare esperienza con arduino, l'lcd tipo 1602 o compatibile e infrarossi. Eseguite con cautela e solo dopo aver controllato 10.000 volte. Questo è di solo studio, L'autore non si ritiene responsabile per qualsiasi danno a cose o persone.
  by redmaxone@gmail.com
