# Fritzing sketch id661_nightlight_0 (saved by Fritzing 0.7.12b)
breadboards: 1

parts:
  Arduino1 = Arduino
  R1 = Photocell (LDR) [package=THT]
  R2 = Resistor [tolerance=±5% resistance=10k package=THT]

nets:
  N1: Arduino1.+5V, R1.pin_0
  N2: Arduino1.GND, R2.Pin_1
  N3: Arduino1.A0, R1.pin_1, R2.Pin_0
