# Fritzing sketch id662_dht11_lcd2x16_yun_0 (saved by Fritzing 0.9.0b)
breadboards: 1

parts:
  Εξάρτημα1 = Arduino Yun
  LCD1 = LCD screen
  R1 = Resistor [tolerance=±5% resistance=4.7k package=THT]
  DHT1 = DHT11_Temperature_and_Humitidy_Sensor
  R2 = Resistor [tolerance=±5% resistance=10k package=THT]

nets:
  5V: Εξάρτημα1.5V, LCD1.VDD, LCD1.LED+, DHT1.connector1
  N1: Εξάρτημα1.D8, DHT1.connector2, R2.Pin_0
  N2: Εξάρτημα1.D11_PWM/MOSI, LCD1.E
  N3: Εξάρτημα1.D12/MISO, LCD1.RS
  N4: Εξάρτημα1.D2, LCD1.DB7
  N5: Εξάρτημα1.D3_PWM, LCD1.DB6
  N6: Εξάρτημα1.D4, LCD1.DB5
  N7: Εξάρτημα1.D5_PWM, LCD1.DB4
  GND: Εξάρτημα1.GND, LCD1.VSS, LCD1.R/W, LCD1.LED-, R1.Pin_1, DHT1.connector4, R2.Pin_1
  N8: LCD1.V0, R1.Pin_0

notes:
  I just used as many colours as I ad.
