# Fritzing sketch id665_Arduino_Project_0 (saved by Fritzing 0.8.7b)
breadboards: 1

parts:
  Part1 = Arduino Uno (Rev3)
  LED1 = RGB LED (com. anode, rbg) [package="5 mm [THT]"]
  R1 = Resistor [tolerance=±5% resistance=10k package=THT]
  J1 = Piezo Speaker
  U1 = POT [package=alps_pot]
  R2 = Resistor [tolerance=±5% resistance=220 package=THT]
  R3 = Resistor [tolerance=±5% resistance=10k package=THT]
  R4 = Resistor [tolerance=±5% resistance=10k package=THT]
  R5 = Resistor [tolerance=±5% resistance=10k package=THT]
  R6 = Resistor [tolerance=±5% resistance=10k package=THT]
  R7 = Resistor [tolerance=±5% resistance=10k package=THT]
  R8 = Resistor [tolerance=±5% resistance=10k package=THT]
  R9 = Resistor [tolerance=±5% resistance=10k package=THT]
  R10 = Resistor [tolerance=±5% resistance=10k package=THT]
  R11 = Resistor [tolerance=±5% resistance=10k package=THT]
  R12 = Resistor [tolerance=±5% resistance=10k package=THT]
  R13 = Resistor [tolerance=±5% resistance=10k package=THT]
  R14 = Resistor [tolerance=±5% resistance=10k package=THT]
  S1 = Pushbutton [package="[THT]"]
  U2 = RELAY-2 [package=relay-g5v]
  R15 = PHOTOCELL [package=photocell-kit]
  R16 = Resistor [tolerance=±5% resistance=10k package=THT]
  R17 = Resistor [tolerance=±5% resistance=330 package=THT]  # not connected

nets:
  N1: Part1.D10_PWM/SS, J1.pin1
  N2: Part1.D12/MISO, S1.Pin_1, S1.Pin_2
  N3: Part1.GND, R1.Pin_0, U1.S, R2.Pin_1, R9.Pin_0, R10.Pin_0, R11.Pin_0, R12.Pin_0, R13.Pin_0, R14.Pin_0, U2.5, R16.Pin_0
  N4: Part1.D4, U2.6
  N5: Part1.D7, R15.P$2, R16.Pin_1
  N6: LED1.common_anode, R1.Pin_1
  N7: J1.pin2, U1.A
  N8: R3.Pin_1, R9.Pin_1
  N9: R4.Pin_1, R10.Pin_1
  N10: R5.Pin_1, R11.Pin_1
  N11: R6.Pin_1, R12.Pin_1
  N12: R7.Pin_1, R14.Pin_1
  N13: R8.Pin_1, R13.Pin_1
  N14: S1.Pin_3, S1.Pin_4, R15.P$1
