# Fritzing sketch id666_Diagram_for_wiring_0 (saved by Fritzing 0.9.3b)
breadboards: 1

parts:
  Part1 = Arduino Uno (Rev3) - ICSP
  Part2 = Bluetooth HC-05 Macho
  IC1 = L293D [package=THT]
  M1 = DC Motor
  M2 = DC Motor
  LED1 = LEDs [package=led10mm]
  LED2 = LEDs [package=led10mm]

nets:
  N1: Part1.ICSP_MISO, Part1.D12/MISO, LED2.A
  N2: Part1.D8, IC1.In_3
  N3: Part1.D9_PWM, IC1.In_4
  N4: Part1.D11_PWM/MOSI, LED1.C
  GND: Part1.GND, Part2.GND, IC1.0V, LED1.A, LED2.C
  N5: Part1.D0/RX, Part2.TXD
  N6: Part1.D1/TX, Part2.RXD
  N7: Part1.D3_PWM, IC1.In_1
  N8: Part1.D4, IC1.In_2
  N9: Part1.D6_PWM, IC1.Enable_1
  N10: Part1.5V, IC1.+Vmotor, IC1.+V
  N11: IC1.Out_1_(_Controlled_by_Enable_1_), M2.pin_2
  N12: IC1.Out_2_(_Controlled_by_Enable_1_), M2.pin_1
  N13: IC1.Out_3_(_Controlled_by_Enable_2_), M1.pin_2
  N14: IC1.Out_4_(_Controlled_by_Enable_2_), M1.pin_1
