# Fritzing sketch id667_Arduino_Servo_Knob_0 (saved by Fritzing 0.7.12b)
breadboards: 1

parts:
  Arduino1 = Arduino
  R1 = Trimmer Potentiometer [maximum_resistance=10kΩ package=THT]
  J1 = Basic Servo

nets:
  N1: Arduino1.D9, J1.pulse
  +5V: Arduino1.+5V, R1.leg1, J1.vcc
  GND: Arduino1.GND, R1.leg2, J1.gnd
  N2: Arduino1.A0, R1.wiper
