# Fritzing sketch id669_Arduino_Servo_Knob2_cds_0 (saved by Fritzing 0.7.12b)
breadboards: 1

parts:
  Arduino1 = Arduino
  J1 = Basic Servo
  J2 = Basic Servo
  R2 = Resistor [tolerance=±5% resistance=10k package=THT]
  R3 = Photocell (LDR) [package=THT]

nets:
  N1: Arduino1.D10, J2.pulse
  N2: Arduino1.D9, J1.pulse
  +5V: Arduino1.+5V, J1.vcc, R2.Pin_0
  GND: Arduino1.GND, J1.gnd, R3.pin_1
  N3: Arduino1.A0, R2.Pin_1, R3.pin_0
