# Fritzing sketch id671_ARDUINO_UNO_+_10_LED_0 (saved by Fritzing 0.7.5b)

parts:
  Arduino1 = Arduino
  LED1 = LED - 3mm [color="Blue (525nm)" package="3 mm [THT]"]
  LED2 = LED - 3mm [color="Blue (525nm)" package="3 mm [THT]"]
  LED3 = LED - 3mm [color="Blue (525nm)" package="3 mm [THT]"]
  LED4 = LED - 3mm [color="Blue (525nm)" package="3 mm [THT]"]
  LED5 = LED - 3mm [color="Blue (525nm)" package="3 mm [THT]"]
  LED6 = LED - 3mm [color="Blue (525nm)" package="3 mm [THT]"]
  LED7 = LED - 3mm [color="Blue (525nm)" package="3 mm [THT]"]
  LED8 = LED - 3mm [color="Blue (525nm)" package="3 mm [THT]"]
  LED9 = LED - 3mm [color="Blue (525nm)" package="3 mm [THT]"]
  LED10 = LED - 3mm [color="Blue (525nm)" package="3 mm [THT]"]
  R6 = Resistor [tolerance=±5% resistance=220 package=THT]
  R8 = Resistor [tolerance=±5% resistance=220 package=THT]
  R10 = Resistor [tolerance=±5% resistance=220 package=THT]
  R7 = Resistor [tolerance=±5% resistance=220 package=THT]
  R9 = Resistor [tolerance=±5% resistance=220 package=THT]
  R4 = Resistor [tolerance=±5% resistance=220 package=THT]
  R5 = Resistor [tolerance=±5% resistance=220 package=THT]
  R2 = Resistor [tolerance=±5% resistance=220 package=THT]
  R3 = Resistor [tolerance=±5% resistance=220 package=THT]
  R1 = Resistor [tolerance=±5% resistance=220 package=THT]

nets:
  N1: Arduino1.D9, R1.Pin_0
  N2: Arduino1.D8, R3.Pin_0
  N3: Arduino1.D7, R2.Pin_0
  N4: Arduino1.D6, R5.Pin_0
  N5: Arduino1.D5, R4.Pin_0
  N6: Arduino1.D4, R9.Pin_0
  N7: Arduino1.D3, R7.Pin_0
  N8: Arduino1.D2, R6.Pin_0
  N9: Arduino1.D1TX, R8.Pin_0
  N10: Arduino1.D0RX, R10.Pin_0
  N11: LED1.anode, LED2.cathode, LED2.anode, R1.Pin_1
  N12: LED3.cathode, LED4.anode, R2.Pin_1
  N13: LED4.cathode, R3.Pin_1
  N14: LED5.cathode, R9.Pin_1
  N15: LED5.anode, LED8.cathode, R7.Pin_1
  N16: LED6.cathode, R5.Pin_1
  N17: LED6.anode, LED7.cathode, LED7.anode, R4.Pin_1
  N18: LED8.anode, LED9.cathode, R6.Pin_1
  N19: LED9.anode, LED10.cathode, LED10.anode, R8.Pin_1, R10.Pin_1

notes:
  Nothing big here, excepting that you have to solder leds and resistors all together instead of using a breadboard. I don't like breadboards this is the reason why I solder.
  The code I used on ARDUINO 1.0.1 is an array code with my own values in it :
  /*
  Arrays
  Demonstrates the use of an array to hold pin numbers
  in order to iterate over the pins in a sequence.
  Lights multiple LEDs in sequence, then in reverse.
  Unlike the For Loop tutorial, where the pins have to be
  contiguous, here the pins can be in any random order.
  The circuit:
  * LEDs from pins 2 through 7 to ground
  created 2006
  by David A. Mellis
  modified 30 Aug 2011
  by Tom Igoe
  This example code is in the public domain.
  http://www.arduino.cc/en/Tutorial/Array
  */
  int timer = 100; // The higher the number, the slower the timing.
  int ledPins[] = {
  0, 1, 2, 3, 4, 5, 6, 7, 8, 9 }; // an array of pin numbers to which LEDs are attached
  int pinCount = 10; // the number of pins (i.e. the length of the array)
  void setup() {
  int thisPin;
  // the array elements are numbered from 0 to (pinCount - 1).
  // use a for loop to initialize each pin as an output:
  for (int thisPin = 0; thisPin < pinCount; thisPin++) {
  pinMode(ledPins[thisPin], OUTPUT);
  }
  }
  void loop() {
  // loop from the lowest pin to the highest:
  for (int thisPin = 0; thisPin < pinCount; thisPin++) {
  // turn the pin on:
  digitalWrite(ledPins[thisPin], HIGH);
  delay(timer);
  // turn the pin off:
  digitalWrite(ledPins[thisPin], HIGH);
  }
  // loop from the highest pin to the lowest:
  for (int thisPin = pinCount - 0; thisPin >= 0; thisPin--) {
  // turn the pin on:
  digitalWrite(ledPins[thisPin], HIGH);
  delay(timer);
  // turn the pin off:
  digitalWrite(ledPins[thisPin], LOW);
  }
  }
