# Fritzing sketch id673_ARDUINO_UNO_+_JOYSTICK_SHIELD_+_8_OHM_SPEAKER_0 (saved by Fritzing 0.7.5b)

parts:
  Arduino2 = Arduino  # not connected
  Composants2 = Arduino Joystick Shield
  SPKR1 = Loudspeaker [part_number="8 OHM SPEAKER"]  # not connected
  R1 = Resistor [tolerance=±1% resistance=100 package=THT]

nets:
  N1: Composants2.SEL, R1.Pin_1

notes:
  THIS is a simple project that allows you to distort, accelerate, or slow down the tempo of a binary sound via a joystick.
  The resistor is a 100 ohm.
  If you push the joystick on the left, you will slow down the tempo.
  If you push the joystick on the right, you will accelerate the tempo.
  If you push the joystick up, you will go up in the treble.
  If you push the joystick down, you will go down in the bass.
  THE CODE you have to copy and paste into the ARDUINO software is :
  /*
  JoystickArduinoMelodyControl.pde
  A sketch to demonstrate using a joystick to control the
  tempo and pitch of a "melody".
  (And you thought the standard Melody sketch was annoying!)
  How to use:
  * Connect joystick shield to your Arduino
  * Connect piezo buzzer to your Arduino using breadboard and jumper wire
  * Positive pin of buzzer to Arduino pin 9
  * Other pin of buzzer to Arduino ground (GND)
  * Upload this sketch to your Arduino
  * Move joystick
  * Moving left and right controls the tempo
  * Moving up and down controls the pitch
  Requires:
  * Arduino
  * SparkFun Joystick Shield
  This sketch is a lightly modified version of<http://www.arduino.cc/en/Tutorial/Melody>
  for SparkFun Arduino Inventor's Kit CIRC-JOY
  */
  // Store the Arduino pin associated with each axis of the joystick input
  const byte PIN_ANALOG_X = 0;
  const byte PIN_ANALOG_Y = 1;
  const int speakerPin = 2;
  int length = 15; // the number of notes
  char notes[] = "ccggaagffeeddc "; // a space represents a rest
  int beats[] = { 1, 1, 1, 1, 1, 1, 2, 1, 1, 1, 1, 1, 1, 2, 4 };
  int tempo = 300;
  void playTone(int tone, int duration) {
  for (long i = 0; i < duration * 1000L; i += tone * 2) {
  digitalWrite(speakerPin, HIGH);
  delayMicroseconds(tone);
  digitalWrite(speakerPin, LOW);
  delayMicroseconds(tone);
  }
  }
  void playNote(char note, int duration) {
  char names[] = { 'c', 'd', 'e', 'f', 'g', 'a', 'b', 'C' };
  int tones[] = { 1915, 1700, 1519, 1432, 1275, 1136, 1014, 956 };
  // play the tone corresponding to the note name
  for (int i = 0; i < 8; i++) {
  if (names[i] == note) {
  // We modify the pitch of the note to be played based on the vertical position
  // of the joystick:
  playTone(tones[i] + map(analogRead(PIN_ANALOG_Y), 0, 1023, 959, -959), duration);
  }
  }
  }
  void setup() {
  pinMode(speakerPin, OUTPUT);
  }
  void loop() {
  for (int i = 0; i < length; i++) {
  // We set the tempo based on the horizontal position of the joystick:
  tempo = map(analogRead(PIN_ANALOG_X), 0, 1023, 500, 100);
  if (notes[i] == ' ') {
  delay(beats[i] * tempo); // rest
  } else {
  playNote(notes[i], beats[i] * tempo);
  }
  // pause between notes
  delay(tempo / 2);
  }
  }
