# Fritzing sketch id674_Breadboard_Sketch_0 (saved by Fritzing 0.7.12b)
breadboards: 1

parts:
  MIDI-OUT = DIN-5 jack (MIDI) [package=THT]
  MIDI-IN = DIN-5 jack (MIDI) [package=THT]
  R9 = Resistor [tolerance=±5% resistance=220 package=THT]
  D1 = Rectifier Diode [part_number=1N4001 package="300 mil [THT]"]
  6N138 = IC, DIP package, 8 pins [chip_label=6N138]
  R10 = Resistor [tolerance=±5% resistance=270 package=THT]
  Arduino1 = Arduino
  R8 = Resistor [tolerance=±5% resistance=220 package=THT]
  GB_LINK_IN = shrouded pin header, 6 pins [form="♂ (shrouded male)"]
  LED1 = LED - 5mm [color="Red (633nm)" package="5 mm [THT]"]
  LED2 = LED - 5mm [color="Red (633nm)" package="5 mm [THT]"]
  LED3 = LED - 5mm [color="Red (633nm)" package="5 mm [THT]"]
  LED4 = LED - 5mm [color="Red (633nm)" package="5 mm [THT]"]
  LED5 = LED - 5mm [color="Red (633nm)" package="5 mm [THT]"]
  R1 = Resistor [tolerance=±5% resistance=2k package=THT]
  R2 = Resistor [tolerance=±5% resistance=2k package=THT]
  R3 = Resistor [tolerance=±5% resistance=2k package=THT]
  R4 = Resistor [tolerance=±5% resistance=2k package=THT]
  R5 = Resistor [tolerance=±5% resistance=2k package=THT]
  R6 = Resistor [tolerance=±5% resistance=2k package=THT]
  R7 = Resistor [tolerance=±5% resistance=2k package=THT]
  BTN1 = Pushbutton [package=THT]
  LEDSTATUS = LED - 5mm [color="Green (555nm)" package="5 mm [THT]"]

nets:
  N1: MIDI-OUT.5, R8.Pin_1
  N2: MIDI-OUT.2, GB_LINK_IN.pin3
  N3: MIDI-OUT.4, Arduino1.D1TX
  N4: MIDI-IN.5, D1.anode, 6N138.pin3
  N5: MIDI-IN.4, R9.Pin_0
  N6: R9.Pin_1, D1.cathode
  N7: 6N138.pin5, LED1.cathode, LED2.cathode, LED3.cathode, LED4.cathode, LED5.cathode, R7.Pin_1, LEDSTATUS.cathode
  N8: 6N138.pin6, R10.Pin_1, Arduino1.D0RX
  N9: 6N138.pin8, R10.Pin_0, Arduino1.D4
  N10: Arduino1.D12, R5.Pin_1
  N11: Arduino1.D11, R4.Pin_1
  N12: Arduino1.D10, R3.Pin_1
  N13: Arduino1.D9, R2.Pin_1
  N14: Arduino1.D8, R1.Pin_1
  N15: Arduino1.D3, R7.Pin_0, BTN1.leg0
  N16: Arduino1.VIN, GB_LINK_IN.pin6
  N17: Arduino1.A0, GB_LINK_IN.pin4
  N18: Arduino1.A1, GB_LINK_IN.pin5
  N19: Arduino1.A2, GB_LINK_IN.pin1
  N20: R8.Pin_0, BTN1.leg1
  N21: LED1.anode, R1.Pin_0
  N22: LED2.anode, R2.Pin_0
  N23: LED3.anode, R3.Pin_0
  N24: LED4.anode, R4.Pin_0
  N25: LED5.anode, R5.Pin_0
  N26: R6.Pin_0, LEDSTATUS.anode

notes:
  GB LINK IN
  optional 5V into Arduino
