# Fritzing sketch id675_Arduino_ISP_Shield_v1.0_0 (saved by Fritzing 0.7.5b)
breadboards: 1

parts:
  28-Pin_ZIF_Socket = 28_Pin_ZIF_Socket_from_SparkFun
  R1 = Resistor [tolerance=±5% resistance=10k package=THT]
  XTAL1 = Crystal [frequency="16 Mhz" package=THT]
  C1 = Ceramic Capacitor [capacitance=100nF package="100 mil [THT, multilayer]"]
  C2 = Ceramic Capacitor [capacitance=100nF package="100 mil [THT, multilayer]"]
  24/44/84 = IC, DIP package, 12 pins [chip_label=24/44/84 spacing=300mil part_number=ATtiny]
  328 = IC, DIP package, 6 pins [chip_label=328 spacing=300mil part_number=ATmega]
  25/45/85 = IC, DIP package, 12 pins [chip_label=25/45/85 spacing=300mil part_number=ATtiny]
  Arduino1 = Arduino [part_number=ATTiny]
  R2 = Resistor [tolerance=±5% resistance=10k package=THT]
  J2 = male pin header, 1 pin [form="♂ (male)"]
  C3 = Electrolytic Capacitor [capacitance=10µF voltage=25V package="100 mil [THT, electrolytic]"]
  Blink = LED - 3mm [color="White (6500K)" part_number=LED package="3 mm [THT]"]
  Reset = Pushbutton [package="[THT]"]
  328_2 = male pin header, 1 pin [form="♂ (male)"]
  *5 = male pin header, 1 pin [form="♂ (male)"]
  J1 = male pin header, 1 pin [form="♂ (male)"]

nets:
  N1: 28-Pin_ZIF_Socket.connector0, 24/44/84.pin12, 328.pin4, 25/45/85.pin7
  N2: 28-Pin_ZIF_Socket.connector2, 328_2.pin1
  N3: 28-Pin_ZIF_Socket.connector3, 24/44/84.pin7, 25/45/85.pin11
  N4: 28-Pin_ZIF_Socket.connector6, 24/44/84.pin10, 328.pin6
  N5: 28-Pin_ZIF_Socket.connector7, C1.0, C2.1, 24/44/84.pin2, 328.pin2, 25/45/85.pin2, Arduino1.GND, R2.Pin_0, C3.-, Reset.Pin_3, Reset.Pin_4
  N6: 28-Pin_ZIF_Socket.connector8, XTAL1.pin_0, C1.1
  N7: 28-Pin_ZIF_Socket.connector9, XTAL1.pin_1, C2.0
  N8: 28-Pin_ZIF_Socket.connector16, 24/44/84.pin3, 25/45/85.pin3, Arduino1.D11
  N9: 28-Pin_ZIF_Socket.connector17, 24/44/84.pin4, 25/45/85.pin4, Arduino1.D12
  N10: 28-Pin_ZIF_Socket.connector18, 24/44/84.pin5, 25/45/85.pin5, Arduino1.D13
  N11: 28-Pin_ZIF_Socket.connector19, R1.Pin_0, 24/44/84.pin1, 328.pin1, 25/45/85.pin1, Arduino1.+5V
  N12: 28-Pin_ZIF_Socket.connector21, 24/44/84.pin9, 328.pin5
  N13: 28-Pin_ZIF_Socket.connector22, 24/44/84.pin8
  N14: 28-Pin_ZIF_Socket.connector24, 25/45/85.pin10
  N15: 28-Pin_ZIF_Socket.connector25, 25/45/85.pin9, *5.pin1
  N16: 28-Pin_ZIF_Socket.connector26, 25/45/85.pin8
  N17: 28-Pin_ZIF_Socket.connector27, 24/44/84.pin11, 25/45/85.pin12
  N18: R1.Pin_1, 24/44/84.pin6, 328.pin3, 25/45/85.pin6, Arduino1.D10, Reset.Pin_1, Reset.Pin_2
  N19: Arduino1.RST, C3.+
  N20: R2.Pin_1, Blink.cathode
  N21: J2.pin1, Blink.anode, J1.pin1

notes:
  Crystal + Capacitors for ATMega328
  3 Sets of DIP switches for:
  - ATTiny25/45/85
  - ATTiny24/44/84
  - ATMega328p
  ArduinoISP
  www.jeffmurchison.com
  Deluxe v1.0
  DIP SWITCHES
  | ** Turn on ONLY ONE group ** |
  | ** of switches at a time! ** |
  ATtiny
  ATmega
  ------------------------------
  Sorry, the schematic view is a total mess. I really need to fix it.
  Description: An Arduino shield to be used for programming/bootloading ATtiny
  and ATmega microconrollers.
  Author: Jeff Murchison
  Contact: jeff@jeffmurchison.com
  Date: July 11, 2012
  Version: 1.0
  License:
  This work is licensed under a Creative Commons Attribution-NonCommercial-ShareAlike 3.0 Unported License:
  http://creativecommons.org/licenses/by-nc-sa/3.0/
  You are free to:
  Share — to copy, distribute and transmit the work
  Remix — to adapt the work
  Under the following conditions:
  Attribution — You must attribute the work in the manner specified by the author or licensor (but not in any way that suggests that they endorse you or your use of the work).
  Noncommercial — You may not use this work for commercial purposes.
  Share Alike — If you alter, transform, or build upon this work, you may distribute the resulting work only under the same or similar license to this one.
  ------
  Notes: May require a custom part (ZIF socket).
  If you have any questions, comments, or if you've made some awesome changes to my design, feel free to send me an email!
  You can also BUY one of these shields (provided any are in stock) at:
  https://tindie.com/jeffmurchison/
