# Fritzing sketch id676_Arduino_ISP_Shield_v2.0_0 (saved by Fritzing 0.7.5b)
breadboards: 1

parts:
  R2 = Resistor [tolerance=±5% resistance=10k package=THT]
  16MHz = Crystal [frequency="16 Mhz" package=THT]
  C2 = Ceramic Capacitor [capacitance=100nF package="100 mil [THT, multilayer]"]
  C1 = Ceramic Capacitor [capacitance=100nF package="100 mil [THT, multilayer]"]
  24/44/84 = IC, DIP package, 12 pins [chip_label=24/44/84 spacing=300mil part_number=ATtiny]
  Arduino1 = Arduino [part_number=ATTiny]
  R1 = Resistor [tolerance=±5% resistance=10k package=THT]
  C3 = Electrolytic Capacitor [capacitance=10µF voltage=25V package="100 mil [THT, electrolytic]"]
  Blink = LED - 3mm [color="White (6500K)" part_number=LED package="3 mm [THT]"]
  Reset = Pushbutton [package="[THT]"]
  25/45/85/*313 = IC, DIP package, 12 pins [chip_label=25/45/85/2313 spacing=300mil part_number=ATtiny]
  Heart = LED - 3mm [color="White (6500K)" part_number=beat package="3 mm [THT]"]
  Error = LED - 3mm [color="White (6500K)" package="3 mm [THT]"]
  Prog = LED - 3mm [color="White (6500K)" package="3 mm [THT]"]
  ZIF_Socket1 = 28_Pin_ZIF_Socket_from_SparkFun [part_number=PRT-09175]
  168/328 = IC, DIP package, 12 pins [chip_label=328 spacing=300mil part_number=ATmega]
  R3 = Resistor [tolerance=±5% resistance=10k package=THT]
  R4 = Resistor [tolerance=±5% resistance=10k package=THT]
  R5 = Resistor [tolerance=±5% resistance=10k package=THT]
  328 = double row male pin header, 4 pins [form="♂ (male)"]
  Auto = male pin header, 3 pins [form="♂ (male)" part_number=Reset]
  328_2 = male pin header, 3 pins [form="♂ (male)"]
  328_3 = male pin header, 3 pins [form="♂ (male)"]
  328_4 = male pin header, 3 pins [form="♂ (male)"]

nets:
  N1: R2.Pin_0, 24/44/84.pin1, Arduino1.+5V, 25/45/85/*313.pin1, 168/328.pin4
  N2: R2.Pin_1, 24/44/84.pin6, Arduino1.D10, Reset.Pin_1, Reset.Pin_2, 25/45/85/*313.pin6, 168/328.pin6
  N3: 16MHz.pin_0, C2.1, 168/328.pin1
  N4: 16MHz.pin_1, C1.0, 168/328.pin2
  N5: C2.0, C1.1, 24/44/84.pin2, Arduino1.GND, R1.Pin_1, C3.-, Reset.Pin_3, Reset.Pin_4, 25/45/85/*313.pin2, 168/328.pin5, R3.Pin_0, R4.Pin_0, R5.Pin_0
  N6: 24/44/84.pin3, Arduino1.D11, 25/45/85/*313.pin3, ZIF_Socket1.connector16
  N7: 24/44/84.pin4, Arduino1.D12, 25/45/85/*313.pin4, ZIF_Socket1.connector17
  N8: 24/44/84.pin5, Arduino1.D13, 25/45/85/*313.pin5, 168/328.pin3
  N9: 24/44/84.pin7, 25/45/85/*313.pin11, 328_2.pin2
  N10: 24/44/84.pin8, ZIF_Socket1.connector22
  N11: 24/44/84.pin9, ZIF_Socket1.connector21, 168/328.pin8, 328_4.pin2
  N12: 24/44/84.pin10, ZIF_Socket1.connector19, 168/328.pin9, 328_3.pin2
  N13: 24/44/84.pin11, 25/45/85/*313.pin12, ZIF_Socket1.connector27
  N14: 24/44/84.pin12, 25/45/85/*313.pin7, ZIF_Socket1.connector0, 168/328.pin7
  N15: Arduino1.D9, Heart.anode
  N16: Arduino1.D8, Error.anode
  N17: Arduino1.D7, Prog.anode
  N18: Arduino1.RST, Auto.pin2
  N19: R1.Pin_0, Blink.cathode
  N20: C3.+, Auto.pin3
  N21: Blink.anode, 328.pin2, 328.pin3
  N22: 25/45/85/*313.pin8, ZIF_Socket1.connector26
  N23: 25/45/85/*313.pin9, ZIF_Socket1.connector25, 328.pin1
  N24: 25/45/85/*313.pin10, ZIF_Socket1.connector24
  N25: Heart.cathode, R5.Pin_1
  N26: Error.cathode, R4.Pin_1
  N27: Prog.cathode, R3.Pin_1
  N28: ZIF_Socket1.connector2, 328.pin4
  N29: ZIF_Socket1.connector3, 328_2.pin1
  N30: ZIF_Socket1.connector6, 328_3.pin1
  N31: ZIF_Socket1.connector7, 328_4.pin1
  N32: ZIF_Socket1.connector8, 168/328.pin12
  N33: ZIF_Socket1.connector9, 168/328.pin11, 328_2.pin3
  N34: ZIF_Socket1.connector18, 168/328.pin10

notes:
  Crystal + Capacitors for ATMega328
  3 Sets of DIP switches for:
  - ATTiny25/45/85
  - ATTiny24/44/84
  - ATMega328p
  ArduinoISP
  Deluxe v2.0
  DIP SWITCHES
  | ** Turn on ONLY ONE group at a time! ** |
  ATtiny
  ATmega &
  ------------------------------------------
  Sorry, the schematic view is a total mess. I really need to fix it.
  Description: An Arduino shield to be used for programming/bootloading ATtiny
  and ATmega microconrollers.
  Author: Jeff Murchison
  Contact: jeff@jeffmurchison.com
  Date: July 11, 2012
  Version: 1.0
  License:
  This work is licensed under a Creative Commons Attribution-NonCommercial-ShareAlike 3.0 Unported License:
  http://creativecommons.org/licenses/by-nc-sa/3.0/
  You are free to:
  Share — to copy, distribute and transmit the work
  Remix — to adapt the work
  Under the following conditions:
  Attribution — You must attribute the work in the manner specified by the author or licensor (but not in any way that suggests that they endorse you or your use of the work).
  Noncommercial — You may not use this work for commercial purposes.
  Share Alike — If you alter, transform, or build upon this work, you may distribute the resulting work only under the same or similar license to this one.
  ------
  Notes: May require a custom part (ZIF socket).
  If you have any questions, comments, or if you've made some awesome changes to my design, feel free to send me an email!
  You can also BUY one of these shields (provided any are in stock) at:
  https://tindie.com/jeffmurchison/
  ATtiny *313
  *4 / *5
  OFF
  ON
  --
  ---
  ATtiny *4/*5
  & ATmega
  -
  ----
