# Fritzing sketch id677_Arduino_ISP_Shield_v2.5e_0 (saved by Fritzing 0.7.12b)

parts:
  Arduino2 = Arduino [part_number=ATTiny]
  R1 = Resistor [tolerance=±5% resistance=10k package=THT]
  R5 = Resistor [tolerance=±5% resistance=10k package=THT]
  R4 = Resistor [tolerance=±5% resistance=10k package=THT]
  R3 = Resistor [tolerance=±5% resistance=10k package=THT]
  R2 = Resistor [tolerance=±5% resistance=10k package=THT]
  16MHz = Crystal [frequency="16 Mhz" package=THT]
  C1 = Ceramic Capacitor [capacitance=22pF package="100 mil [THT, multilayer]"]
  C2 = Ceramic Capacitor [capacitance=22pF voltage=10V package="100 mil [THT, multilayer]"]
  25/45/85/*314 = IC, DIP package, 12 pins [spacing=300mil part_number=ATtiny chip_label=25/45/85/*314]
  168/329 = IC, DIP package, 12 pins [chip_label=328 spacing=300mil part_number=ATmega]
  24/44/85 = IC, DIP package, 12 pins [chip_label=24/44/84 spacing=300mil part_number=ATtiny]
  328 = male pin header, 3 pins [form="♂ (male)"]
  328_2 = male pin header, 3 pins [form="♂ (male)"]
  328_3 = male pin header, 3 pins [form="♂ (male)"]
  Blink = LED - 3mm [color="White (6500K)" part_number=LED package="3 mm [THT]"]
  C3 = Electrolytic Capacitor [capacitance=10µF voltage=25V package="100 mil [THT, electrolytic]"]
  Reset = Pushbutton [package="[THT]"]
  Prog = LED - 3mm [color="White (6500K)" package="3 mm [THT]"]
  Error = LED - 3mm [color="White (6500K)" package="3 mm [THT]"]
  Heart = LED - 3mm [color="White (6500K)" part_number=beat package="3 mm [THT]"]
  Auto = male pin header, 3 pins [form="♂ (male)" part_number=Reset]
  28-Pin_ZIF_Socket = 28_Pin_ZIF_Socket_from_SparkFun [part_number=PRT-09175]

nets:
  N1: Arduino2.GND, R1.Pin_1, R5.Pin_0, R4.Pin_0, R3.Pin_0, C1.1, C2.0, 25/45/85/*314.pin2, 168/329.pin5, 24/44/85.pin2, C3.-, Reset.Pin_3, Reset.Pin_4
  N2: Arduino2.D13, 25/45/85/*314.pin5, 168/329.pin3, 24/44/85.pin5
  N3: Arduino2.D12, 25/45/85/*314.pin4, 24/44/85.pin4, 28-Pin_ZIF_Socket.connector17
  N4: Arduino2.D11, 25/45/85/*314.pin3, 24/44/85.pin3, 28-Pin_ZIF_Socket.connector16
  N5: Arduino2.D10, R2.Pin_1, 25/45/85/*314.pin6, 168/329.pin6, 24/44/85.pin6, Reset.Pin_1, Reset.Pin_2
  N6: Arduino2.D9, Heart.anode
  N7: Arduino2.D8, Error.anode
  N8: Arduino2.D7, Prog.anode
  N9: Arduino2.RST, Auto.pin2
  N10: Arduino2.+5V, R2.Pin_0, 25/45/85/*314.pin1, 168/329.pin4, 24/44/85.pin1
  N11: R1.Pin_0, Blink.cathode
  N12: R5.Pin_1, Heart.cathode
  N13: R4.Pin_1, Error.cathode
  N14: R3.Pin_1, Prog.cathode
  N15: 16MHz.pin_0, C2.1, 168/329.pin1
  N16: 16MHz.pin_1, C1.0, 168/329.pin2
  N17: 25/45/85/*314.pin7, 168/329.pin7, 24/44/85.pin12, 28-Pin_ZIF_Socket.connector0
  N18: 25/45/85/*314.pin8, 28-Pin_ZIF_Socket.connector26
  N19: 25/45/85/*314.pin9, 28-Pin_ZIF_Socket.connector25
  N20: 25/45/85/*314.pin10, 28-Pin_ZIF_Socket.connector24
  N21: 25/45/85/*314.pin11, 24/44/85.pin7, 328_3.pin2
  N22: 25/45/85/*314.pin12, 24/44/85.pin11, 28-Pin_ZIF_Socket.connector27
  N23: 168/329.pin8, 24/44/85.pin9, 328.pin2, 28-Pin_ZIF_Socket.connector21
  N24: 168/329.pin9, 24/44/85.pin10, 328_2.pin2, 28-Pin_ZIF_Socket.connector19
  N25: 168/329.pin10, 28-Pin_ZIF_Socket.connector18
  N26: 168/329.pin11, 328_3.pin3, 28-Pin_ZIF_Socket.connector9
  N27: 168/329.pin12, 28-Pin_ZIF_Socket.connector8
  N28: 24/44/85.pin8, 28-Pin_ZIF_Socket.connector22
  N29: 328.pin1, 28-Pin_ZIF_Socket.connector7
  N30: 328_2.pin1, 28-Pin_ZIF_Socket.connector6
  N31: 328_3.pin1, 28-Pin_ZIF_Socket.connector3
  N32: Blink.anode, 28-Pin_ZIF_Socket.connector2
  N33: C3.+, Auto.pin3

notes:
  Deluxe v2.5
  ArduinoISP
  ATmega168/328
  ATtiny24/44/84
  ATtiny25/45/85/*313
  *313
  --
  Other
  ATtiny
  ON
  ---
  OFF
  ------------------------------------------
  | ** Turn on ONLY ONE group at a time! ** |
  This view is still being cleaned up.
