# Fritzing sketch id678_ArduinoISP_Zif28_0 (saved by Fritzing 0.7.0b)
breadboards: 1

parts:
  R1 = Resistor [resistance=1k tolerance=±5% package=THT]
  RESET = Pushbutton [package="[THT]"]
  R2 = Resistor [resistance=220 tolerance=±5% package=THT]
  R3 = Resistor [resistance=220 tolerance=±5% package=THT]
  R4 = Resistor [resistance=220 tolerance=±5% package=THT]
  R5 = Resistor [resistance=220 tolerance=±5% package=THT]
  OSC = Resonator [frequency="16 Mhz" package=THT]
  IC2 = IC, DIP package, 28 pins [chip_label=IC spacing=600mil]
  Arduino_ISP = Arduino
  HELLO = smd LED [color="Green (555nm)" package="1206 [SMD]"]
  LED1 = smd LED [color="Green (555nm)" package="1206 [SMD]"]
  LED2 = smd LED [color="Red (633nm)" package="1206 [SMD]"]
  LED3 = smd LED [color="Yellow (585nm)" package="1206 [SMD]"]

nets:
  5V: R1.Pin_0, IC2.pin7, IC2.pin20, Arduino_ISP.+5V
  N1: R1.Pin_1, RESET.Pin_1, RESET.Pin_2, IC2.pin1, Arduino_ISP.D10
  GND: RESET.Pin_3, RESET.Pin_4, R2.Pin_0, R3.Pin_1, R4.Pin_1, R5.Pin_1, OSC.GND, IC2.pin8, IC2.pin22, Arduino_ISP.GND
  N2: R2.Pin_1, HELLO.cathode
  N3: R3.Pin_0, LED1.cathode
  N4: R4.Pin_0, LED2.cathode
  N5: R5.Pin_0, LED3.cathode
  N6: OSC.0, IC2.pin9
  N7: OSC.pin_1, IC2.pin10
  N8: IC2.pin14, HELLO.anode
  N9: IC2.pin17, Arduino_ISP.D11
  N10: IC2.pin18, Arduino_ISP.D12
  N11: IC2.pin19, Arduino_ISP.D13
  N12: Arduino_ISP.D9, LED1.anode
  N13: Arduino_ISP.D8, LED2.anode
  N14: Arduino_ISP.D7, LED3.anode

notes:
  Using an Arduino as ISP:
  http://arduino.cc/en/Tutorial/ArduinoISP
