# Fritzing sketch id680_ArduinoMeister_0 (saved by Fritzing 0.9.2b)
breadboards: 1
perfboards: 1

parts:
  Bauteil1 = Arduino Leonardo (Rev3b)
  DIN1 = DIN-5 jack (MIDI) [package=THT]
  DIN2 = DIN-5 jack (MIDI) [package=THT]
  R1 = Resistor [tolerance=±5% resistance=220 package="0402 [SMD]"]
  R2 = Resistor [tolerance=±5% resistance=220 package="0402 [SMD]"]
  IC1 = IC, DIP package, 8 pins [chip_label=6N138]
  R3 = Resistor [tolerance=±5% resistance=10k package="0402 [SMD]"]
  R4 = Resistor [tolerance=±5% resistance=470 package="0402 [SMD]"]
  D1 = Rectifier Diode [part_number=1N4001 package="300 mil [THT]"]
  R5 = Resistor [tolerance=±5% resistance=220 package="0402 [SMD]"]
  J1 = female pin header, 5 pins [form="♀ (female)"]

nets:
  N1: Bauteil1.D0/RX, IC1.pin6, R4.Pin_0
  N2: Bauteil1.D1/TX, R2.Pin_0
  N3: Bauteil1.5V, R1.Pin_0, IC1.pin8, R4.Pin_1, J1.pin1
  N4: Bauteil1.GND, DIN1.2, DIN2.2, IC1.pin5, R3.Pin_0, J1.pin2
  N5: Bauteil1.D8/A8, J1.pin5
  N6: Bauteil1.D9_PWM/A9, J1.pin4
  N7: Bauteil1.D10_PWM/A10, J1.pin3
  N8: DIN1.5, IC1.pin3, D1.anode
  N9: DIN1.4, R5.Pin_1
  N10: DIN2.5, R2.Pin_1
  N11: DIN2.4, R1.Pin_1
  N12: IC1.pin2, D1.cathode, R5.Pin_0
  N13: IC1.pin7, R3.Pin_1

notes:
  MIDI-OUT -> AMP
  7-pin DIN
  Pin 7: GND
  Pin 6: +20V (150 mA)
  DC/DC Wandler LM2596
  MIDI-IN
  5-pin DIN
  TM138
  1 - VCC / 2 - GND / 3 - STB / 4 - CLK / 6 -DIO
  Hughes & Kettner - GrandMeister 36 MIDI Control
