# Fritzing sketch id681_HomeDuino_uP_SensorPad_2015_09_25_prototype_0 (saved by Fritzing 0.9.0b)
circuit board: 4.5cm x 4.5cm

parts:
  RS485_Shield = KP_RS485_Modul
  Arduino_Nano_V3 = Arduino Nano (Rev3.0)
  5V_Regultr = Voltage Regulator - 5V [package="TO220 [THT]"]
  J2_Bus = screw terminal, 2 pins
  J1_Power = screw terminal, 2 pins
  R5 = Resistor [tolerance=±0.05% resistance=10k package=THT]
  R4 = Resistor [tolerance=±5% resistance=10k package=THT]
  R3 = Resistor [tolerance=±5% resistance=10k package=THT]
  R2 = Resistor [tolerance=±5% resistance=10k package=THT]
  R1 = Resistor [tolerance=±5% resistance=10k package=THT]
  R0 = Resistor [tolerance=±5% resistance=10k package=THT]
  J4_A0-5 = screw terminal, 3 pins
  J4_A0-6 = screw terminal, 3 pins
  GND_GND = screw terminal, 2 pins
  J5 = screw terminal, 4 pins
  J3 = female pin header, 4 pins [form="♀ (female)"]
  J4 = female pin header, 4 pins [form="♀ (female)"]

nets:
  GND: RS485_Shield.connector0, Arduino_Nano_V3.GND, 5V_Regultr.GND, J1_Power.pin1, R5.Pin_1, R4.Pin_1, R3.Pin_1, R2.Pin_1, R1.Pin_1, R0.Pin_1, J3.pin2
  N1: RS485_Shield.connector1, J2_Bus.pin1
  N2: RS485_Shield.connector2, J2_Bus.pin2
  N3: RS485_Shield.connector3, Arduino_Nano_V3.5V, 5V_Regultr.output_voltage, GND_GND.pin1, GND_GND.pin2, J3.pin1
  N4: RS485_Shield.connector4, Arduino_Nano_V3.D3
  N5: RS485_Shield.connector5, RS485_Shield.connector6, Arduino_Nano_V3.D8
  N6: RS485_Shield.connector7, Arduino_Nano_V3.D2
  N7: Arduino_Nano_V3.D4, J5.pin4, J4.pin4
  N8: Arduino_Nano_V3.D5, J5.pin3, J4.pin3
  N9: Arduino_Nano_V3.D6, J5.pin2, J4.pin2
  N10: Arduino_Nano_V3.D7, J5.pin1, J4.pin1
  N11: Arduino_Nano_V3.A5, R5.Pin_0, J4_A0-5.pin1, J3.pin4
  N12: Arduino_Nano_V3.A4, R4.Pin_0, J4_A0-5.pin2, J3.pin3
  N13: Arduino_Nano_V3.A3, R3.Pin_0, J4_A0-5.pin3
  N14: Arduino_Nano_V3.A2, R2.Pin_0, J4_A0-6.pin1
  N15: Arduino_Nano_V3.A1, R1.Pin_0, J4_A0-6.pin2
  N16: Arduino_Nano_V3.A0, R0.Pin_0, J4_A0-6.pin3
  N17: 5V_Regultr.input_voltage, J1_Power.pin2

notes:
  1
  A
  GND
  5V  5V
  ICSP Anschluß
  Arduino nano
  Pin D6 - D9 + 5V + GND
  Schraubanschluß für D4 D5
  Jumper für D4
  Jumper für D5
  5V Festspannung
  Bus und Vin + GND
  RS485 Shield
  Pins A1 - A4
  B
  A3   A4   A5
  A0   A1   A2
  B   A
  GND  Vi
  D7  D6   D5  D4
  DEPin: 8 - DIpin: 2 - ROpin: D3
  D7 D6 D5 D4
  V5 GND A4 A5
  kduino 09/2015
  mail@kurtpetzuch.de
