# Fritzing sketch id682_ArduinoNanoISP_0 (saved by Fritzing 0.9.0b)
circuit board: 8.46667cm x 5.64444cm
breadboards: 1

parts:
  Part1 = Arduino Nano (Rev3.0)
  R1 = Resistor [tolerance=±5% resistance=10k package=THT]
  Y1 = Resonator [frequency="16 Mhz" package=THT]
  ZIF_SOCKET1 = Aries 28-6574-10 28W ZIF Socket [part_number=28-6574-10]
  U1 = atmega328 [package=dip]

nets:
  GND: Part1.GND, Y1.GND, ZIF_SOCKET1.Pin_8, ZIF_SOCKET1.Pin_22, U1.GND
  N1: Part1.D10, R1.Pin_1, ZIF_SOCKET1.Pin_1, U1.RESET
  N2: Part1.D11/MOSI, ZIF_SOCKET1.Pin_18, U1.D12
  N3: Part1.D12/MISO, ZIF_SOCKET1.Pin_17, U1.D11_(PWM)
  5V: Part1.5V, R1.Pin_0, ZIF_SOCKET1.Pin_7, ZIF_SOCKET1.Pin_20, U1.VCC, U1.AVCC
  N4: Part1.D13/SCK, ZIF_SOCKET1.Pin_19, U1.D13
  N5: Y1.0, ZIF_SOCKET1.Pin_9, U1.XLAT1
  N6: Y1.pin_1, ZIF_SOCKET1.Pin_10, U1.XLAT2
  N7: ZIF_SOCKET1.Pin_2, U1.D0_(RX)
  N8: ZIF_SOCKET1.Pin_3, U1.D1_(TX)
  N9: ZIF_SOCKET1.Pin_4, U1.D2
  N10: ZIF_SOCKET1.Pin_5, U1.D3_(PWM)
  N11: ZIF_SOCKET1.Pin_6, U1.D4
  N12: ZIF_SOCKET1.Pin_11, U1.D5_(PWM)
  N13: ZIF_SOCKET1.Pin_12, U1.D6_(PWM)
  N14: ZIF_SOCKET1.Pin_13, U1.D7
  N15: ZIF_SOCKET1.Pin_14, U1.D8
  N16: ZIF_SOCKET1.Pin_15, U1.D9_(PWM)
  N17: ZIF_SOCKET1.Pin_16, U1.D10_(PWM)
  N18: ZIF_SOCKET1.Pin_21, U1.AREF
  N19: ZIF_SOCKET1.Pin_23, U1.A0
  N20: ZIF_SOCKET1.Pin_24, U1.A1
  N21: ZIF_SOCKET1.Pin_25, U1.A2
  N22: ZIF_SOCKET1.Pin_26, U1.A3
  N23: ZIF_SOCKET1.Pin_27, U1.A4
  N24: ZIF_SOCKET1.Pin_28, U1.A5
