# Fritzing sketch id683_Arduino_nrf_0 (saved by Fritzing 0.9.2b)
breadboards: 1

parts:
  Composant2 = Arduino Pro Mini v13
  DHT = TMP36 [package=to-92]
  U3 = 2.4GHz Low Power Transceiver [package=qfn20]
  IC1 = V_REG_LD1117VXX [package=78xxl]
  Composant3 = Arduino Uno (Rev3) - ICSP
  U4 = 2.4GHz Low Power Transceiver [package=qfn20]
  Composant4 = Arduino Color LCD Shield

nets:
  GND: Composant2.GND, DHT.GND, IC1.OUT
  VCC: Composant2.VCC, DHT.VCC, IC1.IN
  N1: Composant2.A0, DHT.VOUT
  N2: Composant2.D13/SCK, U3.MOSI
  N3: Composant2.D12/MISO, U3.IRQ
  N4: Composant2.D11_PWM/MOSI, U3.MISO
  N5: Composant2.D8, U3.CSN
  N6: Composant2.D7, U3.SCK
  N7: U3.XC2, IC1.GND
  N8: Composant3.ICSP_MISO, Composant3.D12/MISO, U4.IRQ
  N9: Composant3.ICSP_MOSI, Composant3.D11_PWM/MOSI, U4.MISO
  GND_2: Composant3.GND, U4.VSS, Composant4.GND
  N10: Composant3.D8, U4.CSN
  N11: Composant3.D13/SCK, U4.MOSI
  N12: Composant3.D3_PWM, Composant4.D9
  N13: Composant3.D4, Composant4.D10
  N14: Composant3.D5_PWM, Composant4.D11
  N15: Composant3.D6_PWM, Composant4.D12
  N16: Composant3.D7, U4.SCK, Composant4.D13
  3V3: Composant3.3V3, U4.XC2, Composant4.D8, Composant4.3.3V
