# Fritzing sketch id684_arduinorc.1.2a_0 (saved by Fritzing 0.7.10b)
breadboards: 1

parts:
  POT6 = Rotary Potentiometer (Small) [maximum_resistance=10kΩ]
  POT5 = Rotary Potentiometer (Small) [maximum_resistance=10kΩ]
  POT4 = Rotary Potentiometer (Small) [maximum_resistance=10kΩ]
  POT3 = Rotary Potentiometer (Small) [maximum_resistance=10kΩ]
  POT2 = Rotary Potentiometer (Small) [maximum_resistance=10kΩ]
  POT1 = Rotary Potentiometer (Small) [maximum_resistance=10kΩ]
  SwModel = Pushbutton [package=THT]
  SwMode = Pushbutton [package=THT]
  SwThrottle = Pushbutton [package=THT]
  SwRate = Pushbutton [package=THT]
  ConnectRF = screw terminal, 4 pins
  SwBind = Pushbutton [package=THT]
  R1 = Resistor [tolerance=±5% resistance=12k package=THT]
  R2 = Resistor [tolerance=±5% resistance=10k package=THT]
  R3 = Resistor [tolerance=±5% resistance=270 package=THT]
  Nano1 = Arduino Nano v3.0
  LED1 = LED - 5mm [color="Red (633nm)" package="5 mm [THT]"]
  Sw1 = Pushbutton [package=THT]
  R4 = Resistor [tolerance=±5% resistance=47k package=THT]
  R5 = Resistor [tolerance=±5% resistance=47k package=THT]
  Piezo1 = Piezo Speaker
  R3_2 = Resistor [tolerance=±5% resistance=220 package=THT]
  U1 = Voltage Regulator - 5V [package="TO220 [THT]"]
  VCC = Battery block 9V
  SwMain = Pushbutton [package=THT]
  C2 = Ceramic Capacitor [capacitance=0.33µF package="100 mil [THT, multilayer]"]
  C1 = Ceramic Capacitor [capacitance=100nF package="100 mil [THT, multilayer]"]

nets:
  GND: POT6.leg1, POT5.leg1, POT4.leg1, POT3.leg1, POT2.leg1, POT1.leg1, SwModel.leg0, SwMode.leg0, SwThrottle.leg0, SwRate.leg0, ConnectRF.pin4, SwBind.leg0, R2.Pin_0, R3.Pin_1, Nano1.GND, Sw1.leg0, R4.Pin_1, Piezo1.pin1, U1.GND, VCC.-, C2.0, C1.0
  N1: POT6.wiper, Nano1.A5
  N2: POT6.leg2, POT5.leg2, POT4.leg2, POT3.leg2, POT2.leg2, POT1.leg2, ConnectRF.pin3, Nano1.+5V, U1.output_voltage, C1.1
  N3: POT5.wiper, Nano1.A4
  N4: POT4.wiper, Nano1.A3
  N5: POT3.wiper, Nano1.A2
  N6: POT2.wiper, Nano1.A1
  N7: POT1.wiper, Nano1.A0
  N8: SwModel.leg1, Nano1.D8
  N9: SwMode.leg1, Nano1.D9
  N10: SwThrottle.leg1, Nano1.D11
  N11: SwRate.leg1, Nano1.D12
  N12: ConnectRF.pin1, R1.Pin_1, R2.Pin_1
  N13: ConnectRF.pin2, SwBind.leg1
  N14: R1.Pin_0, Nano1.D10
  N15: R3.Pin_0, LED1.cathode
  N16: Nano1.D2, Sw1.leg1
  N17: Nano1.D7, R3_2.Pin_1
  N18: Nano1.D13, LED1.anode
  N19: Nano1.A7, R4.Pin_0, R5.Pin_1
  N20: R5.Pin_0, U1.input_voltage, SwMain.leg0, C2.1
  N21: Piezo1.pin2, R3_2.Pin_0
  N22: VCC.+, SwMain.leg1

notes:
  Gnd
  +5v
  Bind
  PPM
  Arduino Radio Control
  6 channels RC transmitter
  http://www.reseau.org/arduinorc
  3 Sep 2013 - version 1.2
  Arduino Radio Control - 6 channels RC transmitter
  3 Sep 2013 - v 1.2 - http://www.reseau.org/arduinorc
