# Fritzing sketch id685_ArduinoServo_0 (saved by Fritzing 0.9.3b)

parts:
  Part1 = Arduino Uno (Rev3)
  J1 = Basic Servo

nets:
  N1: Part1.D9_PWM, J1.pulse
  GND: Part1.GND, J1.gnd
  5V: Part1.5V, J1.vcc
