# Fritzing sketch id686_Arduped_Bach_0 (saved by Fritzing 0.9.3b)
breadboards: 1

parts:
  Arduino_nano = Arduino Nano (Rev3.0)
  J1 = Basic Servo
  J2 = Basic Servo
  J3 = Basic Servo
  J4 = Basic Servo
  J5 = Basic Servo
  Ping = Infrared Proximity Sensor
  V1 = DC Power [voltage=5]

nets:
  GND: Arduino_nano.GND, Ping.GND
  N1: Arduino_nano.D2, Ping.Vout
  N2: Arduino_nano.D3, J5.pulse
  N3: Arduino_nano.D4, J4.pulse
  N4: Arduino_nano.D5, J3.pulse
  N5: Arduino_nano.D6, J2.pulse
  N6: Arduino_nano.D7, J1.pulse
  N7: Arduino_nano.5V, V1.V+
  N8: J1.gnd, V1.V-
  VCC: J1.vcc, Ping.Vcc
