# Fritzing sketch id687_camera_1_0_0 (saved by Fritzing 0.9.1b)
breadboards: 1

parts:
  Part2 = Arduino Ethernet Shield (Rev3)
  U1 = Optocoupler [package=THT]
  R1 = Resistor [tolerance=±5% resistance=600 package=THT]
  U2 = 2.5mm Audio Jack [package=stereojack2.5mm_specia_pogopins]
  U4 = RF-LINK_RX [package=rf-link_rx]

nets:
  N1: Part2.D8, R1.Pin_0
  N2: Part2.D2, U4.DATA
  5V: Part2.5V, U4.+5V
  GND: Part2.GND, U1.Pin_2, U4.GND
  N3: U1.Pin_1, R1.Pin_1
  N4: U1.Pin_4, U2.SLEEVE
  N5: U1.Pin_5, U2.LEFT, U2.RIGHT
