# Fritzing sketch id691_BUS_i2C_0 (saved by Fritzing 0.7.11b)
breadboards: 1

parts:
  R1 = Resistor [tolerance=±5% resistance=220 package=THT]
  R2 = Resistor [tolerance=±5% resistance=220 package=THT]
  J5 = Screw terminal - 2 pins [package=THT]
  J6 = Screw terminal - 2 pins [package=THT]
  J7 = Screw terminal - 2 pins [package=THT]
  J3 = Screw terminal - 2 pins [package=THT]
  J2 = Screw terminal - 2 pins [package=THT]
  J1 = Screw terminal - 2 pins [package=THT]
  J4 = screw terminal, 2 pins

nets:
  5V: R1.Pin_0, R2.Pin_0, J7.pin1
  N1: R1.Pin_1, J5.pin2, J6.pin2, J3.pin2, J2.pin2, J1.pin2, J4.pin2
  N2: R2.Pin_1, J5.pin1, J6.pin1, J3.pin1, J2.pin1, J1.pin1, J4.pin1
  GND: J7.pin2

notes:
  -
  +
  I2C
