# Fritzing sketch id692_Capteur_analog_2_digital_0 (saved by Fritzing 0.7.11b)
breadboards: 1

parts:
  J1 = screw terminal, 4 pins
  J2 = screw terminal, 4 pins
  J3 = screw terminal, 4 pins
  J4 = screw terminal, 4 pins
  LED1 = LED - 3mm [color="Red (633nm)" package="3 mm [THT]"]
  R1 = Resistor [tolerance=±5% resistance=220 package=THT]
  U1 = LM 358 Dual Op-Amp [package="DIP8 [THT]"]
  LED2 = LED - 3mm [color="Red (633nm)" package="3 mm [THT]"]
  R2 = Resistor [tolerance=±5% resistance=220 package=THT]
  J5 = shrouded pin header, 10 pins [form="♂ (shrouded male)"]
  R4 = Rotary Potentiometer (Small) [maximum_resistance=100kΩ]
  R3 = Rotary Potentiometer (Small) [maximum_resistance=10kΩ]
  U2 = LM 358 Dual Op-Amp [package="DIP8 [THT]"]
  LED3 = LED - 3mm [color="Red (633nm)" package="3 mm [THT]"]
  R5 = Resistor [tolerance=±5% resistance=220 package=THT]
  LED4 = LED - 3mm [color="Red (633nm)" package="3 mm [THT]"]
  R6 = Resistor [tolerance=±5% resistance=220 package=THT]
  R7 = Rotary Potentiometer (Small) [maximum_resistance=100kΩ]
  R8 = Rotary Potentiometer (Small) [maximum_resistance=100kΩ]
  LED5 = LED - 3mm [color="Red (633nm)" package="3 mm [THT]"]
  LED6 = LED - 3mm [color="Red (633nm)" package="3 mm [THT]"]
  R9 = Resistor [tolerance=±5% resistance=220 package=THT]
  R10 = Resistor [tolerance=±5% resistance=220 package=THT]
  U3 = LM 358 Dual Op-Amp [package="DIP8 [THT]"]
  R11 = Rotary Potentiometer (Small) [maximum_resistance=100kΩ]
  R12 = Rotary Potentiometer (Small) [maximum_resistance=100kΩ]
  LED7 = LED - 3mm [color="Red (633nm)" package="3 mm [THT]"]
  LED8 = LED - 3mm [color="Red (633nm)" package="3 mm [THT]"]
  R13 = Resistor [tolerance=±5% resistance=220 package=THT]
  R14 = Resistor [tolerance=±5% resistance=220 package=THT]
  U4 = LM 358 Dual Op-Amp [package="DIP8 [THT]"]
  R15 = Rotary Potentiometer (Small) [maximum_resistance=100kΩ]
  R16 = Rotary Potentiometer (Small) [maximum_resistance=100kΩ]
  DC_Power1 = DC Power [voltage=5]
  C3 = Ceramic Capacitor [capacitance=100nF package="200 mil [THT, multilayer]"]
  C2 = Ceramic Capacitor [capacitance=100nF package="200 mil [THT, multilayer]"]
  C4 = Ceramic Capacitor [capacitance=100nF package="200 mil [THT, multilayer]"]
  C1 = Ceramic Capacitor [capacitance=100nF package="200 mil [THT, multilayer]"]

nets:
  5V: J1.pin1, J2.pin1, J3.pin1, J4.pin1, LED1.anode, U1.connector7, LED2.anode, J5.pin1, R4.leg1, R3.leg1, U2.connector7, LED3.anode, LED4.anode, R7.leg1, R8.leg1, LED5.anode, LED6.anode, U3.connector7, R11.leg1, R12.leg1, LED7.anode, LED8.anode, U4.connector7, R15.leg1, R16.leg1, DC_Power1.V+, C3.1, C2.1, C4.1, C1.1
  GND: J1.pin2, J2.pin2, J3.pin2, J4.pin2, U1.connector3, J5.pin10, R4.leg2, R3.leg2, U2.connector3, R7.leg2, R8.leg2, U3.connector3, R11.leg2, R12.leg2, U4.connector3, R15.leg2, R16.leg2, DC_Power1.GND, C3.0, C2.0, C4.0, C1.0
  N1: J1.pin3, U1.connector5
  N2: J1.pin4, U1.connector1
  N3: J2.pin3, U2.connector5
  N4: J2.pin4, U2.connector1
  N5: J3.pin3, U3.connector5
  N6: J3.pin4, U3.connector1
  N7: J4.pin3, U4.connector5
  N8: J4.pin4, U4.connector1
  N9: LED1.cathode, R1.Pin_0
  N10: R1.Pin_1, U1.connector0, J5.pin3
  N11: U1.connector2, R3.wiper
  N12: U1.connector4, R4.wiper
  N13: U1.connector6, R2.Pin_1, J5.pin2
  N14: LED2.cathode, R2.Pin_0
  N15: J5.pin4, U2.connector6, R6.Pin_1
  N16: J5.pin5, U2.connector0, R5.Pin_1
  N17: J5.pin6, R9.Pin_1, U3.connector6
  N18: J5.pin7, R10.Pin_1, U3.connector0
  N19: J5.pin8, R13.Pin_1, U4.connector6
  N20: J5.pin9, R14.Pin_1, U4.connector0
  N21: U2.connector2, R8.wiper
  N22: U2.connector4, R7.wiper
  N23: LED3.cathode, R5.Pin_0
  N24: LED4.cathode, R6.Pin_0
  N25: LED5.cathode, R9.Pin_0
  N26: LED6.cathode, R10.Pin_0
  N27: U3.connector2, R11.wiper
  N28: U3.connector4, R12.wiper
  N29: LED7.cathode, R13.Pin_0
  N30: LED8.cathode, R14.Pin_0
  N31: U4.connector2, R15.wiper
  N32: U4.connector4, R16.wiper

notes:
  +
  -
  ARIG
  2
  1
  Ana 2 Dig
