# Fritzing sketch id693_Capteur_micro_switch_0 (saved by Fritzing 0.7.11b)
breadboards: 1

parts:
  R1 = Resistor [tolerance=±5% resistance=10k package=THT]
  R2 = Resistor [tolerance=±5% resistance=10k package=THT]
  LED1 = LED - 3mm [color="Red (633nm)" package="3 mm [THT]"]
  J1 = shrouded pin header, 10 pins [form="♂ (shrouded male)"]
  R3 = Resistor [tolerance=±5% resistance=10k package=THT]
  R4 = Resistor [tolerance=±5% resistance=10k package=THT]
  LED2 = LED - 3mm [color="Red (633nm)" package="3 mm [THT]"]
  R5 = Resistor [tolerance=±5% resistance=10k package=THT]
  R6 = Resistor [tolerance=±5% resistance=10k package=THT]
  LED3 = LED - 3mm [color="Red (633nm)" package="3 mm [THT]"]
  R7 = Resistor [tolerance=±5% resistance=10k package=THT]
  R8 = Resistor [tolerance=±5% resistance=10k package=THT]
  R9 = Resistor [tolerance=±5% resistance=10k package=THT]
  R10 = Resistor [tolerance=±5% resistance=10k package=THT]
  LED5 = LED - 3mm [color="Red (633nm)" package="3 mm [THT]"]
  R11 = Resistor [tolerance=±5% resistance=10k package=THT]
  R12 = Resistor [tolerance=±5% resistance=10k package=THT]
  LED6 = LED - 3mm [color="Red (633nm)" package="3 mm [THT]"]
  R13 = Resistor [tolerance=±5% resistance=10k package=THT]
  R14 = Resistor [tolerance=±5% resistance=10k package=THT]
  LED7 = LED - 3mm [color="Red (633nm)" package="3 mm [THT]"]
  R15 = Resistor [tolerance=±5% resistance=10k package=THT]
  R16 = Resistor [tolerance=±5% resistance=10k package=THT]
  LED8 = LED - 3mm [color="Red (633nm)" package="3 mm [THT]"]
  J5 = screw terminal, 4 pins
  J4 = screw terminal, 4 pins
  J2 = screw terminal, 3 pins
  LED4 = LED - 3mm [color="Red (633nm)" package="3 mm [THT]"]

nets:
  5V: R1.Pin_0, R2.Pin_0, J1.pin1, R3.Pin_0, R4.Pin_0, R5.Pin_0, R6.Pin_0, R7.Pin_0, R8.Pin_0, R9.Pin_0, R10.Pin_0, R11.Pin_0, R12.Pin_0, R13.Pin_0, R14.Pin_0, R15.Pin_0, R16.Pin_0
  N1: R1.Pin_1, LED1.anode
  N2: R2.Pin_1, LED1.cathode, J1.pin3, J5.pin1
  N3: J1.pin2, R16.Pin_1, LED8.cathode, J2.pin1
  N4: J1.pin4, R4.Pin_1, LED2.cathode, J5.pin2
  N5: J1.pin5, R6.Pin_1, LED3.cathode, J5.pin3
  N6: J1.pin6, R8.Pin_1, J4.pin1, LED4.cathode
  N7: J1.pin7, R10.Pin_1, LED5.cathode, J4.pin2
  N8: J1.pin8, R12.Pin_1, LED6.cathode, J4.pin3
  N9: J1.pin9, R14.Pin_1, LED7.cathode, J2.pin2
  GND: J1.pin10, J5.pin4, J4.pin4, J2.pin3
  N10: R3.Pin_1, LED2.anode
  N11: R5.Pin_1, LED3.anode
  N12: R7.Pin_1, LED4.anode
  N13: R9.Pin_1, LED5.anode
  N14: R11.Pin_1, LED6.anode
  N15: R13.Pin_1, LED7.anode
  N16: R15.Pin_1, LED8.anode

notes:
  ARIG
  µ Switch
  -
