# Fritzing sketch id694_Carte_S9706_0 (saved by Fritzing 0.7.11b)
breadboards: 1

parts:
  CONN = shrouded pin header, 10 pins [form="♂ (shrouded male)"]
  S9706 = SO08 [chip_label=S9706 package=SO]
  R1 = Resistor [tolerance=±5% resistance=220 package="1206 [SMD]"]
  Range = SIP - 2 pins [chip_label=IC package="SIP (Single Inline) [THT]"]

nets:
  5V: CONN.pin1, S9706.2, Range.pin1
  N1: CONN.pin2, CONN.pin9, S9706.1
  N2: CONN.pin3, CONN.pin8, S9706.7
  N3: CONN.pin4, CONN.pin7, S9706.8
  N4: CONN.pin5, CONN.pin6, S9706.6, R1.Pin_0, Range.pin2
  GND: CONN.pin10, S9706.3, S9706.4, S9706.5, R1.Pin_1
