# Fritzing sketch id695_Carte_codeur_0 (saved by Fritzing 0.7.10b)
breadboards: 1

parts:
  S1 = Toggle Switch [package=THT]
  S2 = Toggle Switch [package=THT]
  R1 = Resistor [tolerance=±5% resistance=2.7k package=THT]
  R2 = Resistor [tolerance=±5% resistance=2.7k package=THT]
  Analog = shrouded pin header, 10 pins [form="♂ (shrouded male)"]
  Dig_+_RST = shrouded pin header, 10 pins [form="♂ (shrouded male)"]
  I2C = Screw terminal - 2 pins [package=THT]
  Alim = screw terminal, 3 pins
  RS232 = Screw terminal - 2 pins [package=THT]
  R3 = Resistor [tolerance=±5% resistance=2.7k package=THT]
  Codeur = shrouded pin header, 10 pins [form="♂ (shrouded male)"]
  Arduino_Nano = Arduino Nano v3.0
  C1 = Ceramic Capacitor [capacitance=10nF package="200 mil [THT, multilayer]"]

nets:
  GND: S1.L1, S2.L1, Alim.pin2, Codeur.pin1, Codeur.pin10, Arduino_Nano.GND, C1.0
  N1: S1.COM, Arduino_Nano.A7
  5V: S1.L2, S2.L2, R1.Pin_0, R2.Pin_0, Alim.pin1, R3.Pin_0, Codeur.pin4, Codeur.pin7, Arduino_Nano.+5V, C1.1
  N2: S2.COM, Arduino_Nano.A6
  N3: R1.Pin_1, Codeur.pin2, Codeur.pin9, Arduino_Nano.D4
  N4: R2.Pin_1, Codeur.pin5, Codeur.pin6, Arduino_Nano.D3
  N5: Analog.pin1, Analog.pin10, Arduino_Nano.A3
  N6: Analog.pin2, Analog.pin9, Arduino_Nano.A2
  N7: Analog.pin3, Analog.pin8, Arduino_Nano.A1
  N8: Analog.pin4, Analog.pin7, Arduino_Nano.A0
  N9: Analog.pin5, Analog.pin6, Arduino_Nano.AREF
  N10: Dig_+_RST.pin1, Arduino_Nano.D13
  N11: Dig_+_RST.pin2, Arduino_Nano.D12
  N12: Dig_+_RST.pin3, Arduino_Nano.D11
  N13: Dig_+_RST.pin4, Arduino_Nano.D10
  N14: Dig_+_RST.pin5, Arduino_Nano.D9
  N15: Dig_+_RST.pin6, Arduino_Nano.D8
  N16: Dig_+_RST.pin7, Arduino_Nano.D7
  N17: Dig_+_RST.pin8, Arduino_Nano.D6
  N18: Dig_+_RST.pin9, Arduino_Nano.D5
  N19: Dig_+_RST.pin10, Arduino_Nano.RST
  N20: I2C.pin1, Arduino_Nano.A5
  N21: I2C.pin2, Arduino_Nano.A4
  N22: Alim.pin3, Arduino_Nano.VIN
  N23: RS232.pin1, Arduino_Nano.D1TX
  N24: RS232.pin2, Arduino_Nano.D0RX
  N25: R3.Pin_1, Codeur.pin3, Codeur.pin8, Arduino_Nano.D2

notes:
  ARIG - Carte codeur
  SDA
  SCL
  GND
  TX
  5V
  RX
  VIN
  ARIG
  2013
  -
  +
  I
  A
  B
