# Fritzing sketch id695_OPEN_DMX_adapter (saved by Fritzing 0.3.16b)
breadboards: 1

parts:
  Arduino1 = Arduino
  IC1 = IC, DIP package, 8 pins [chip_label=IC spacing=300mil]
  R1 = Resistor [resistance=100 package=THT]
  J1 = screw terminal, 3 pins

nets:
  N1: Arduino1.GND, IC1.pin2, IC1.pin5, R1.Pin_1, J1.pin3
  N2: Arduino1.D0RX, IC1.pin4
  N3: Arduino1.+5V, IC1.pin3, IC1.pin8
  N4: IC1.pin1, R1.Pin_0
  N5: IC1.pin6, J1.pin1
  N6: IC1.pin7, J1.pin2

notes:
  MAX485 EPA+
  RS-422/RS-485 Interface IC
  100ohm Resistor
  You can install an entec OPEN DMX Driver and use
  FreeStyler to control your DMX Devices
  any ? email
  desta@usLEDsupply.com
  DMX OUT (+) (-) (GND)
