# Fritzing sketch id699_Art_Project_0 (saved by Fritzing 0.9.3b)
breadboards: 1

parts:
  R1 = Resistor [tolerance=±5% resistance=220 package=THT]
  LED1 = LED - 5mm [color="Red (633nm)" package="5 mm [THT]"]
  VCC1 = Battery
  S1 = Toggle Switch [package=THT]
  U1 = Vibration Motor- ROB-08449 [package=vibe-motor-10mm]

nets:
  N1: R1.Pin_0, S1.L2, U1.-
  N2: R1.Pin_1, LED1.cathode
  N3: LED1.anode, VCC1.-, U1.+
  N4: VCC1.+, S1.COM
