# Fritzing sketch id701_AsciiModbusSlaveArduinoUno_0 (saved by Fritzing 0.9.2b)
circuit board: 8.46667cm x 5.64444cm
breadboards: 1

parts:
  U1 = MAX485 [package=dil08]
  R1 = Resistor [tolerance=±5% resistance=10k package=THT]
  C1 = Ceramic Capacitor [capacitance=100nF package="100 mil [THT, multilayer]"]
  R2 = Resistor [tolerance=±5% resistance=120 package=THT]
  LED1 = LED - 5mm [color="Red (633nm)" package="5 mm [THT]"]
  R3 = Resistor [tolerance=±5% resistance=220 package=THT]
  R4 = Resistor [tolerance=±5% resistance=100 package=THT]
  Parte1 = Arduino Uno (Rev3)

nets:
  N1: U1.RO, R1.Pin_1, Parte1.D0/RX
  N2: U1.RE, U1.DE, R3.Pin_0, Parte1.D2
  N3: U1.DI, Parte1.D1/TX
  GND: U1.GND, C1.0, R4.Pin_0, Parte1.GND
  N4: U1.A, R2.Pin_1
  N5: U1.B, R2.Pin_0
  VCC: U1.VCC, R1.Pin_0, C1.1, LED1.anode, Parte1.5V
  N6: LED1.cathode, R3.Pin_1
