# Fritzing sketch id702_Secuencia_LED_0 (saved by Fritzing 0.9.3b)
breadboards: 1

parts:
  Componente1 = Arduino Uno (Rev3) - ICSP
  S1 = Pushbutton [package="[THT]"]
  S2 = Pushbutton [package="[THT]"]
  S3 = Pushbutton [package="[THT]"]
  S4 = Pushbutton [package="[THT]"]
  LED1 = smd LED [color="Green (570nm)" package="1206 [SMD]"]
  LED2 = smd LED [color="Red (633nm)" package="1206 [SMD]"]
  LED3 = smd LED [color="Green (570nm)" package="1206 [SMD]"]

nets:
  N1: Componente1.D8, S2.Pin_1, S2.Pin_2
  N2: Componente1.D9_PWM, S3.Pin_1, S3.Pin_2
  N3: Componente1.D10_PWM/SS, S4.Pin_1, S4.Pin_2
  N4: Componente1.D4, LED1.anode
  N5: Componente1.D5_PWM, LED2.anode
  N6: Componente1.D6_PWM, LED3.anode
  N7: Componente1.D7, S1.Pin_1, S1.Pin_2
  N8: Componente1.3V3, LED1.cathode, LED2.cathode, LED3.cathode
  N9: Componente1.5V, S1.Pin_3, S1.Pin_4, S2.Pin_3, S2.Pin_4, S3.Pin_3, S3.Pin_4, S4.Pin_3, S4.Pin_4
