# Fritzing sketch id703_Test1_0 (saved by Fritzing 0.9.1b)
circuit board: 8.46667cm x 5.64444cm
breadboards: 1

parts:
  Part1 = Arduino Uno (Rev3)
  M1 = DC Motor

nets:
  N1: Part1.GND, M1.pin_2
  N2: Part1.5V, M1.pin_1
