# Fritzing sketch id705_asynchronous_SR_latch_0 (saved by Fritzing 0.7.0b)
breadboards: 1

parts:
  U1 = Optocoupler [package=THT]
  U2 = Optocoupler [package=THT]
  VCC2 = Battery
  S1 = Toggle Switch [package=THT]
  S2 = Square Pushbutton
  LED1 = LED - 5mm [color="Red (633nm)" package="5 mm [THT]"]
  VCC1 = Battery block 9V

nets:
  N1: U1.Pin_1, U1.Pin_2, U2.Pin_4, S2.leg1, VCC1.-
  N2: U1.Pin_4, LED1.anode
  N3: U1.Pin_5, VCC2.+
  N4: U2.Pin_1, S1.L1
  N5: U2.Pin_2, U2.Pin_5, S2.leg0
  N6: VCC2.-, LED1.cathode
  N7: S1.COM, VCC1.+
