# Fritzing sketch id706_Breaakout_0 (saved by Fritzing 0.7.0b)
breadboards: 1

parts:
  A1 = Triple Axis Accelerometer Breakout - ADXL335
  S1 = Pushbutton [package="[THT]"]
  R1 = Resistor [tolerance=±5% resistance=1k package=THT]

nets:
  N1: A1.VCC, R1.Pin_1
  N2: S1.Pin_1, S1.Pin_2
  N3: S1.Pin_3, S1.Pin_4, R1.Pin_0

notes:
  Atari Breakout Kit
  GamersLabsKits
