# Fritzing sketch id707_Atari_punk_concolse_0 (saved by Fritzing 0.9.2b)
circuit board: 8.9305cm x 11.1498cm
breadboards: 1

parts:
  U1 = 555 Timer [package="DIP8 [THT]"]
  U2 = 555 Timer [package="DIP8 [THT]"]
  U3 = 555 Timer [package="DIP8 [THT]"]
  4017N = HEF4094 [part_number=4017 package="DIP16 [THT]"]
  Power_plug1 = Power plug
  S2 = Toggle Switch [package=THT]
  D1 = Rectifier Diode [part_number=1N4001 package="300 mil [THT]"]
  D2 = Rectifier Diode [part_number=1N4001 package="300 mil [THT]"]
  C2 = Electrolytic Capacitor [capacitance=1µF package="100 mil [THT, electrolytic]"]
  R1 = Rotary Potentiometer (Small) [maximum_resistance=100kΩ package=THT]
  R2 = Resistor [tolerance=±5% resistance=220 package=THT]
  R3 = Rotary Potentiometer (Small) [maximum_resistance=100kΩ package=THT]
  R4 = Rotary Potentiometer (Small) [maximum_resistance=100kΩ package=THT]
  R5 = Rotary Potentiometer (Small) [maximum_resistance=100kΩ package=THT]
  C4 = Electrolytic Capacitor [capacitance=1µF package="100 mil [THT, electrolytic]"]
  R6 = Resistor [tolerance=±5% resistance=220 package=THT]
  R7 = Resistor [tolerance=±5% resistance=220 package=THT]
  R8 = PHOTOCELL [package=photocell]
  R9 = PHOTOCELL [package=photocell]
  R10 = Resistor [tolerance=±5% resistance=220 package=THT]
  S3 = Toggle Switch [package=THT]
  LED1 = LED - 5mm [color="Red (633nm)" package="5 mm [THT]"]
  R11 = Rotary Potentiometer (Small) [maximum_resistance=100kΩ package=THT]
  D3 = Rectifier Diode [part_number=1N4001 package="300 mil [THT]"]
  S4 = Toggle Switch [package=THT]
  LED2 = LED - 5mm [color="Red (633nm)" package="5 mm [THT]"]
  R12 = Rotary Potentiometer (Small) [maximum_resistance=100kΩ package=THT]
  D4 = Rectifier Diode [part_number=1N4001 package="300 mil [THT]"]
  S5 = Toggle Switch [package=THT]
  LED3 = LED - 5mm [color="Red (633nm)" package="5 mm [THT]"]
  R13 = Rotary Potentiometer (Small) [maximum_resistance=100kΩ package=THT]
  D5 = Rectifier Diode [part_number=1N4001 package="300 mil [THT]"]
  S6 = Toggle Switch [package=THT]
  LED4 = LED - 5mm [color="Red (633nm)" package="5 mm [THT]"]
  R14 = Rotary Potentiometer (Small) [maximum_resistance=100kΩ package=THT]
  D6 = Rectifier Diode [part_number=1N4001 package="300 mil [THT]"]
  S7 = Toggle Switch [package=THT]
  LED5 = LED - 5mm [color="Red (633nm)" package="5 mm [THT]"]
  R15 = Rotary Potentiometer (Small) [maximum_resistance=100kΩ package=THT]
  D7 = Rectifier Diode [part_number=1N4001 package="300 mil [THT]"]
  S8 = Toggle Switch [package=THT]
  LED6 = LED - 5mm [color="Red (633nm)" package="5 mm [THT]"]
  R16 = Rotary Potentiometer (Small) [maximum_resistance=100kΩ package=THT]
  D8 = Rectifier Diode [part_number=1N4001 package="300 mil [THT]"]
  S9 = Toggle Switch [package=THT]
  LED7 = LED - 5mm [color="Red (633nm)" package="5 mm [THT]"]
  R17 = Rotary Potentiometer (Small) [maximum_resistance=100kΩ package=THT]
  D9 = Rectifier Diode [part_number=1N4001 package="300 mil [THT]"]
  LED8 = LED - 5mm [color="Red (633nm)" package="5 mm [THT]"]
  R18 = Rotary Potentiometer (Small) [maximum_resistance=100kΩ package=THT]
  D10 = Rectifier Diode [part_number=1N4001 package="300 mil [THT]"]
  R19 = Resistor [tolerance=±5% resistance=220 package=THT]
  D11 = Rectifier Diode [part_number=1N4001 package="300 mil [THT]"]
  D12 = Rectifier Diode [part_number=1N4001 package="300 mil [THT]"]
  D13 = Rectifier Diode [part_number=1N4001 package="300 mil [THT]"]
  D14 = Rectifier Diode [part_number=1N4001 package="300 mil [THT]"]
  D15 = Rectifier Diode [part_number=1N4001 package="300 mil [THT]"]
  D16 = Rectifier Diode [part_number=1N4001 package="300 mil [THT]"]
  D17 = Rectifier Diode [part_number=1N4001 package="300 mil [THT]"]
  C8 = Electrolytic Capacitor [capacitance=1µF package="100 mil [THT, electrolytic]"]
  C9 = Electrolytic Capacitor [capacitance=1µF package="100 mil [THT, electrolytic]"]
  C11 = Ceramic Capacitor [capacitance=100nF package="100 mil [THT, multilayer]"]
  TRS1 = Audio Jack (TRS) 3.5mm [package="4Ucon 08780 [THT]"]
  LED9 = LED - 5mm [color="Red (633nm)" package="5 mm [THT]"]
  LED10 = LED - 5mm [color="Red (633nm)" package="5 mm [THT]"]
  R20 = Resistor [tolerance=±5% resistance=220 package=THT]
  R21 = Resistor [tolerance=±5% resistance=220 package=THT]
  C12 = Electrolytic Capacitor [capacitance=1µF package="100 mil [THT, electrolytic]"]
  S10 = Pushbutton [package=THT]

nets:
  VSS: U1.Ground, U2.Ground, U3.Ground, 4017N.Vss, 4017N.Q6, Power_plug1.GND, C2.-, R5.leg2, R7.Pin_1, R11.leg2, R12.leg2, R13.leg2, R14.leg2, S7.COM, R15.leg2, R16.leg2, R17.leg2, R18.leg2, R19.Pin_1, C8.-, C9.-, C11.1, TRS1.Sleeve, R20.Pin_0, R21.Pin_0, C12.-
  N1: U1.Trigger, U2.Output
  N2: U1.Output, C4.+
  N3: U1.Reset, U1.Vcc_Supply_Voltage, U2.Reset, U2.Vcc_Supply_Voltage, S2.L1, D1.cathode, R3.leg1, R4.leg2, R8.P$1, R9.P$2, LED9.anode, C12.+
  N4: U1.Threshold, U1.Discharge, R3.wiper, R3.leg2, R8.P$2, C8.+
  N5: U2.Trigger, U2.Threshold, R10.Pin_0, D3.cathode, D4.cathode, D5.cathode, D6.cathode, D7.cathode, D8.cathode, D9.cathode, D10.cathode, C9.+
  N6: U2.Discharge, R4.leg1, R4.wiper, R9.P$1, R10.Pin_1
  N7: U3.Trigger, U3.Threshold, U3.Discharge, C2.+, R1.leg1
  N8: U3.Output, 4017N.Q5
  N9: U3.Control_Voltage, C11.0
  N10: U3.Vcc_Supply_Voltage, 4017N.Vdd, S2.L2, D1.anode, R2.Pin_0, LED10.anode
  N11: 4017N.STROBE, S9.COM
  N12: 4017N.DATA, S3.COM
  N13: 4017N.CLOCK, LED8.anode, R18.leg1
  N14: 4017N.Q1, S4.COM
  N15: 4017N.Q2, S5.COM
  N16: 4017N.Q4, S6.COM
  N17: 4017N.Qs, D2.anode
  N18: 4017N.Q's, S8.COM
  N19: 4017N.OE, D2.cathode, D11.cathode, D12.cathode, D13.cathode, D14.cathode, D15.cathode, D16.cathode, D17.cathode
  N20: Power_plug1.VCC, S10.leg1
  N21: S2.COM, S10.leg0
  N22: R1.wiper, R2.Pin_1
  N23: R5.leg1, R6.Pin_1, R7.Pin_0
  N24: R5.wiper, TRS1.Tip
  N25: C4.-, R6.Pin_0
  N26: S3.L1, LED1.anode, R11.leg1
  N27: S3.L2, D12.anode
  N28: LED1.cathode, LED2.cathode, LED3.cathode, LED4.cathode, LED5.cathode, LED6.cathode, LED7.cathode, LED8.cathode, R19.Pin_0
  N29: R11.wiper, D3.anode
  N30: S4.L1, LED2.anode, R12.leg1
  N31: S4.L2, D13.anode
  N32: R12.wiper, D4.anode
  N33: S5.L1, LED3.anode, R13.leg1
  N34: S5.L2, D14.anode
  N35: R13.wiper, D5.anode
  N36: S6.L1, LED4.anode, R14.leg1
  N37: S6.L2, D15.anode
  N38: R14.wiper, D6.anode
  N39: S7.L1, LED5.anode, R15.leg1
  N40: S7.L2, D16.anode
  N41: R15.wiper, D7.anode
  N42: S8.L1, LED6.anode, R16.leg1
  N43: S8.L2, D17.anode
  N44: R16.wiper, D8.anode
  N45: S9.L1, LED7.anode, R17.leg1
  N46: S9.L2, D11.anode
  N47: R17.wiper, D9.anode
  N48: R18.wiper, D10.anode
  N49: LED9.cathode, R21.Pin_1
  N50: LED10.cathode, R20.Pin_1
