# Fritzing sketch id709_APC_556_0 (saved by Fritzing 0.7.7b)
breadboards: 1

parts:
  IC1 = IC, DIP package, 14 pins [chip_label=NE556]
  R1 = Rotary Potentiometer (Small) [maximum_resistance=100kΩ]
  R2 = Rotary Potentiometer (Small) [maximum_resistance=100kΩ]
  C1 = Ceramic Capacitor [capacitance=100nF package="100 mil [THT, multilayer]"]
  R3 = Resistor [tolerance=±5% resistance=1k package=THT]
  C2 = Ceramic Capacitor [capacitance=100nF package="100 mil [THT, multilayer]"]
  SPKR1 = Loudspeaker

nets:
  N1: IC1.pin1, R2.leg1, R3.Pin_0
  N2: IC1.pin2, IC1.pin6, C1.1
  N3: IC1.pin4, R2.wiper
  N4: IC1.pin5, IC1.pin8
  N5: IC1.pin7, C1.0, R3.Pin_1
  N6: IC1.pin9, SPKR1.pin2
  N7: IC1.pin10, IC1.pin14, R1.wiper, R1.leg2
  N8: IC1.pin12, IC1.pin13, C2.0
