# Fritzing sketch id713_Atlas_Pro_mini_0 (saved by Fritzing 0.9.2b)
breadboards: 1

parts:
  IC1 = ULN2003A [package="DIP16 [THT]"]
  R1 = TRIMPOT [part_number=100ohm package=trimpot_pth_s3_lock]
  R2 = TRIMPOT [package=trimpot_pth_s3_lock]
  Power_plug1 = Power plug [part_number="12 Volt"]
  Power_plug2 = Power plug [part_number="5 Volt"]
  J1 = Screw terminal - 2 pins [part_number="Coil B" package=THT]
  C1 = Electrolytic Capacitor [capacitance=47µF voltage=35V part_number=47uf package="100 mil [THT, electrolytic]"]
  C2 = Electrolytic Capacitor [capacitance=47µF voltage=35V part_number="47 uf" package="100 mil [THT, electrolytic]"]
  U1 = mystery part, 16 pins [chip_label="A4988 Stepper"]
  C3 = Electrolytic Capacitor [capacitance=10µF voltage=35V part_number=10uf package="100 mil [THT, electrolytic]"]
  Raspberry_Pi1 = Raspberry Pi 2
  J5 = Screw terminal - 2 pins [part_number="Laser 2" package=THT]
  J6 = Screw terminal - 2 pins [part_number="Laser 1" package=THT]
  J2 = screw terminal, 2 pins

nets:
  N1: IC1.In_1, Raspberry_Pi1.GPIO17
  N2: IC1.In_2, Raspberry_Pi1.GPIO23
  VCC: IC1.In_3, IC1.COM_-_Common, IC1.Out_7, IC1.Out_3, R1.CCW, Power_plug2.VCC, C2.+, U1.pin2, U1.pin3, U1.pin4, U1.pin9, C3.+, Raspberry_Pi1.5V, J5.pin2, J6.pin2
  GND: IC1.0V, Power_plug2.GND, C2.-, U1.pin10, C3.-, Raspberry_Pi1.GND
  N3: IC1.Out_2, R2.CW
  N4: IC1.Out_1, R1.CW
  N5: R1.WIPER, J6.pin1
  N6: R2.WIPER, J5.pin1
  N7: Power_plug1.GND, C1.+, U1.pin15
  N8: Power_plug1.VCC, C1.-, U1.pin16
  N9: J1.pin1, U1.pin14
  N10: J1.pin2, U1.pin13
  N11: U1.pin1, Raspberry_Pi1.GPIO18
  N12: U1.pin5, U1.pin6
  N13: U1.pin7, Raspberry_Pi1.GPIO27
  N14: U1.pin8, Raspberry_Pi1.GPIO22
  N15: U1.pin11, J2.pin1
  N16: U1.pin12, J2.pin2

notes:
  12 Volt
  5 Volt
  Coil A
  Coil B
  Laser 2
  Laser 1
  -
  +
  2 x 100 Ohm
  35v 47uf
  35V 47 uf
  35V 10uf
