# Fritzing sketch id715_atmega1284p_HC_05_perfboard_01_0 (saved by Fritzing 0.9.2b)
perfboards: 1

parts:
  Atmega1284P1 = Atmega1284P
  C1 = Ceramic Capacitor [capacitance=100nF package="100 mil [THT, multilayer]"]
  C2 = Ceramic Capacitor [capacitance=100nF package="100 mil [THT, multilayer]"]
  XTAL1 = Crystal [frequency="16 Mhz" package=THT]
  C3 = Ceramic Capacitor [capacitance=22pF package="100 mil [THT, multilayer]"]
  C4 = Ceramic Capacitor [capacitance=22pF package="100 mil [THT, multilayer]"]
  S1 = Pushbutton [package="[THT]"]
  R1 = Resistor [tolerance=±5% resistance=10k package=THT]
  R2 = Resistor [tolerance=±5% resistance=470 package=THT]
  C5 = Ceramic Capacitor [capacitance=100nF package="100 mil [THT, multilayer]"]
  J1 = FTDI cable [form="♀ (female)"]
  LED1 = smd LED [color="Green (555nm)" package="0603 [SMD]"]
  J2 = female pin header, 16 pins [form="♀ (female)"]
  J3 = female pin header, 7 pins [form="♀ (female)"]
  BAT1 = BC9VPC [package=bc9vpc]
  U1 = LCD-16X2 [package=lcd-16x2_noholes]  # not connected
  Componente1 = Bluetooth HC-05 Macho  # not connected
  R3 = Resistor [tolerance=±5% resistance=4.7k package=THT]
  D1 = Diode [package=diode-hv]
  D2 = Diode [package=diode-hv]
  D3 = Diode [package=diode-hv]
  D4 = Diode [package=diode-hv]
  Componente2 = FTDI Basic Programmer  # not connected
  U2 = SWITCH-SPST-2 [package=switch-spst-vertical]
  LED2 = smd LED [color="Red (633nm)" package="0603 [SMD]"]
  R4 = Resistor [tolerance=±5% resistance=470 package=THT]
  S2 = Pushbutton [package="[THT]"]
  S3 = Pushbutton [package="[THT]"]
  R5 = Resistor [tolerance=±5% resistance=10k package=THT]
  R6 = Resistor [tolerance=±5% resistance=10k package=THT]
  IC2 = V_REG_LD1117VXX [package=78xxl]
  IC1 = Voltage Regulator [package=78xxl]
  D5 = Diode [package=diode-hv]

nets:
  N1: Atmega1284P1.connector0, R2.Pin_0
  N2: C1.0, J1.connector5
  N3: C1.1, S1.Pin_3, S1.Pin_4, R1.Pin_0
  N4: C2.0, C3.1, C4.0, S1.Pin_1, S1.Pin_2, C5.0, J1.connector0, J1.connector1, LED1.cathode, J2.pin1, J2.pin12, J2.pin16, J3.pin4, BAT1.V-, R3.Pin_0, LED2.cathode, R5.Pin_0, R6.Pin_0, IC2.OUT, IC1.GND
  N5: C2.1, R1.Pin_1, C5.1, J3.pin5, S2.Pin_3, S2.Pin_4, S3.Pin_3, S3.Pin_4
  N6: XTAL1.pin_0, C4.1
  N7: XTAL1.pin_1, C3.0
  N8: R2.Pin_1, LED1.anode
  N9: J1.connector2, D1.A
  N10: J2.pin2, J2.pin15
  N11: J2.pin14, R3.Pin_1
  N12: BAT1.V+, U2.O
  N13: D2.A, IC2.IN
  N14: D3.A, IC1.OUT
  N15: D4.A, U2.P, R4.Pin_1, D5.A
  N16: LED2.anode, R4.Pin_0
  N17: S2.Pin_1, S2.Pin_2, R6.Pin_1
  N18: S3.Pin_1, S3.Pin_2, R5.Pin_1

notes:
  FTDI Cable with USB connector
  GND | CTS# | VCC | TX | RX | RTS#
  HC-05 BT module
  EN | VCC | GND | TXD | RXD | STATE
  pin 34 (KEY / CMD)
  EN
  0.1uF
  22pF
  0.22uF
  10kOhm
  470ohm
  4.7kohm
  Battery Power indicator LED
  Green LED program state / reset
  3.3V
  5V
  FTDI
