# Fritzing sketch id716_teensy_atmega_0 (saved by Fritzing 0.9.2b)
breadboards: 2

parts:
  Teensy1 = Teensy 2.0
  U1 = atmega328 [package=dip]

nets:
  GND: Teensy1.GND, U1.GND
  N1: Teensy1.B0, U1.RESET
  N2: Teensy1.B1, U1.D13
  N3: Teensy1.B2, U1.D11_(PWM)
  N4: Teensy1.B3, U1.D12
  VCC: Teensy1.VCC, U1.VCC, U1.AVCC
