# Fritzing sketch id717_MelodyModule_0 (saved by Fritzing 0.8.7b)
circuit board: 4.79778cm x 2.70933cm
breadboards: 1

parts:
  S1 = Pushbutton [package="[THT]"]
  LED1 = LED - 5mm [color="Red (633nm)" package="5 mm [THT]"]
  R1 = Resistor [tolerance=±5% resistance=220 package=THT]
  SPKR1 = Loudspeaker
  VCC1 = Battery
  Bauteil1 = Arduino Uno (Rev3)
  C1 = Electrolytic Capacitor [capacitance=1µF package="100 mil [THT, electrolytic]"]
  U1 = atmega168 [package=dip]

nets:
  N1: S1.Pin_1, S1.Pin_2, U1.D2
  GND: S1.Pin_3, S1.Pin_4, LED1.cathode, SPKR1.pin1, VCC1.-, Bauteil1.GND, C1.-, U1.D4, U1.GND
  N2: LED1.anode, R1.Pin_0
  N3: R1.Pin_1, Bauteil1.D13/SCK, U1.D13
  N4: SPKR1.pin2, U1.D8
  3V: VCC1.+, Bauteil1.5V, U1.VCC, U1.AVCC
  N5: Bauteil1.D10_PWM/SS, U1.RESET
  N6: Bauteil1.D11_PWM/MOSI, U1.D11_(PWM)
  N7: Bauteil1.D12/MISO, U1.D12
  N8: Bauteil1.RESET, C1.+

notes:
  This wires only for programming the atmega 168 after you have programmed remove this!
  1. First load the ArduinoISP on the arduino board
  2. then put 10 uF to use the Arduino as a Programmer!
  3. Select under Tools- Programmer- Arduino as ISP
  4. Select under Board LilliPad Arduino w/AT168
  5. Then start under Tools Burn Bootloader
  6. Now message comes that bootlader is burnimg.
  7. Load MelodyModulprogram and upload it.
  8. Remove the wires from Arduino to breadboard
  9. connect Battery
  10 Wait 10 seconds Melody plays now.
  Each time you press button anoter melody will play.
  When you remove melody wire melody will stay.
  Removing this wire to fix melody!
  Only for programming the Arduino is needed!
  Only Bootloader for Board LilliPad Arduino w/AT168 is for using the atmega168 with internal oszillator!!!
  Here no external resonator is necessary!
  First start needs unfortunally 10 seconds.
  50 Ohm speaker or a 47 Ohm resistor for a 8 Ohm speaker in series!
  MelodyModule, MelodyModul with atmega168, _2
