# Fritzing sketch id718_ECU_0 (saved by Fritzing 0.9.3b)
circuit board: 7.05063cm x 7.0519cm
breadboards: 1

parts:
  ATMega328 = atmega328 [package=dip]
  XTAL1 = Crystal [frequency="16 Mhz" package=THT]
  C2 = Ceramic Capacitor [capacitance=22µF package="0603 [SMD, multilayer]"]
  C3 = Ceramic Capacitor [capacitance=22µF package="0603 [SMD, multilayer]"]
  5VReg = Voltage Regulator - 5V [package="TO220 [THT]"]
  C5 = Electrolytic Capacitor [capacitance=1µF package="100 mil [THT, electrolytic]"]
  SCL/SDA = Header 2 [part_number=PRT-00116 package=jst-2-pth-ns]
  C6 = Ceramic Capacitor [capacitance="100 nF" package="0603 [SMD, multilayer]"]
  R1 = Resistor [tolerance=±5% resistance=10k package=THT]
  Reset = Header 2 [part_number=PRT-00116 package=jst-2-pth-ns]
  S2 = Header 3 [package=screwterminal-3.5mm-3_lock.007s]
  R3 = Resistor [tolerance=±5% resistance=10k package=THT]
  R2 = Resistor [tolerance=±5% resistance=10k package=THT]
  J2 = Power Jack [package=power_jack_pth]
  Power = Header 2 [part_number=PRT-00116 package=jst-2-pth-ns]
  C4 = Electrolytic Capacitor [capacitance=1nF package="100 mil [THT, electrolytic]"]
  S1 = Header 3 [package=screwterminal-3.5mm-3_lock.007s]
  OLED = Header 6 [package=molex-1x6-ra]
  IO = Header 6 [package=molex-1x6-ra]
  FTDI = Header 6 [package=molex-1x6-ra]
  Relays = Header 4 [package=screwterminal-3.5mm-4_lock]

nets:
  N1: ATMega328.RESET, C6.1
  N2: ATMega328.D0_(RX), FTDI.3
  N3: ATMega328.D1_(TX), FTDI.2
  N4: ATMega328.D2, Relays.4
  N5: ATMega328.D3_(PWM), Relays.3
  N6: ATMega328.D4, Relays.2
  N7: ATMega328.VCC, ATMega328.AVCC, ATMega328.AREF, C2.1, C3.1, 5VReg.output_voltage, C5.+, R1.Pin_1, S2.1, R3.Pin_1, R2.Pin_1, S1.1, OLED.5, FTDI.4
  GND: ATMega328.GND, 5VReg.GND, C5.-, C6.0, Reset.1, S2.3, Power.2, C4.-, S1.3, OLED.6, FTDI.1, FTDI.6
  N8: ATMega328.XLAT1, XTAL1.pin_1, C3.0
  N9: ATMega328.XLAT2, XTAL1.pin_0, C2.0
  N10: ATMega328.D5_(PWM), Relays.1
  N11: ATMega328.D6_(PWM), S2.2, R3.Pin_0
  N12: ATMega328.D7, R2.Pin_0, S1.2
  N13: ATMega328.D8, OLED.4
  N14: ATMega328.D9_(PWM), OLED.3
  N15: ATMega328.D10_(PWM), OLED.2
  N16: ATMega328.D11_(PWM), OLED.1
  N17: ATMega328.D12, IO.6
  N18: ATMega328.D13, IO.5
  N19: ATMega328.A0, IO.4
  N20: ATMega328.A1, IO.3
  N21: ATMega328.A2, IO.2
  N22: ATMega328.A3, IO.1
  N23: ATMega328.A4, SCL/SDA.1
  N24: ATMega328.A5, SCL/SDA.2
  N25: 5VReg.input_voltage, J2.PWR, C4.+
  N26: R1.Pin_0, Reset.2
  N27: J2.GND, J2.GNDBREAK, Power.1
