# Fritzing sketch id719_ECUv2_0 (saved by Fritzing 0.9.3b)
circuit board: 5cm x 7cm
breadboards: 1

parts:
  ATMega328 = atmega328 [package=dip]
  5VR = Voltage Regulator - 5V [package="TO220 [THT]"]
  C2 = Electrolytic Capacitor [capacitance=1µF package="100 mil [THT, electrolytic]"]
  R1 = Resistor [tolerance=±5% resistance=10k package=THT]
  R3 = Resistor [tolerance=±5% resistance=10k package=THT]
  R2 = Resistor [tolerance=±5% resistance=10k package=THT]
  7-9V = Power Jack [package=power_jack_pth]
  C1 = Electrolytic Capacitor [capacitance=1nF package="100 mil [THT, electrolytic]"]
  XTAL1 = Crystal [frequency="16 Mhz" package=THT]
  IOA = male pin header, 3 pins [form="♂ (male)"]
  IOB = male pin header, 3 pins [form="♂ (male)"]
  Relays = male pin header, 4 pins [form="♂ (male)"]
  OLED = male pin header, 6 pins [form="♂ (male)"]
  FTDI = male pin header, 6 pins [form="♂ (male)"]
  SCLSDA = male pin header, 2 pins [form="♂ (male)"]
  RST = male pin header, 2 pins [form="♂ (male)"]
  PWR = male pin header, 2 pins [form="♂ (male)"]
  S1 = male pin header, 3 pins [form="♂ (male)"]
  S2 = male pin header, 3 pins [form="♂ (male)"]
  C4 = Ceramic Capacitor [capacitance=22µF package="100 mil [THT, multilayer]"]
  C5 = Ceramic Capacitor [capacitance=22µF package="100 mil [THT, multilayer]"]
  C3 = Ceramic Capacitor [capacitance="100 nF" package="100 mil [THT, multilayer]"]
  R4 = Resistor [tolerance=±5% resistance=10k package=THT]
  LED1 = LED - 3mm [color="Red (633nm)" package="3 mm [THT]"]
  ExtLED = male pin header, 2 pins [form="♂ (male)"]

nets:
  N1: ATMega328.RESET, R1.Pin_0, C3.1
  N2: ATMega328.D0_(RX), FTDI.pin3
  N3: ATMega328.D1_(TX), FTDI.pin2
  N4: ATMega328.D2, IOB.pin1
  N5: ATMega328.D3_(PWM), IOB.pin2
  N6: ATMega328.D4, IOB.pin3
  N7: ATMega328.VCC, ATMega328.AVCC, ATMega328.AREF, R1.Pin_1, FTDI.pin4
  GND: ATMega328.GND, 5VR.GND, C2.-, C1.-, OLED.pin6, FTDI.pin6, RST.pin1, PWR.pin2, S1.pin3, S2.pin3, C4.1, C5.1, LED1.anode, ExtLED.pin2
  N8: ATMega328.XLAT1, XTAL1.pin_1, C4.0
  N9: ATMega328.XLAT2, XTAL1.pin_0, C5.0
  N10: ATMega328.D5_(PWM), Relays.pin1
  N11: ATMega328.D6_(PWM), Relays.pin2
  N12: ATMega328.D7, Relays.pin3
  N13: ATMega328.D8, Relays.pin4
  N14: ATMega328.D9_(PWM), IOA.pin3
  N15: ATMega328.D10_(PWM), OLED.pin4
  N16: ATMega328.D11_(PWM), OLED.pin3
  N17: ATMega328.D12, OLED.pin2
  N18: ATMega328.D13, OLED.pin1
  N19: ATMega328.A0, IOA.pin2
  N20: ATMega328.A1, IOA.pin1
  N21: ATMega328.A2, R3.Pin_0, S2.pin2
  N22: ATMega328.A3, R2.Pin_0, S1.pin2
  N23: ATMega328.A4, SCLSDA.pin2
  N24: ATMega328.A5, SCLSDA.pin1
  N25: 5VR.input_voltage, 7-9V.PWR, C1.+
  N26: 5VR.output_voltage, C2.+, R3.Pin_1, R2.Pin_1, OLED.pin5, S1.pin1, S2.pin1, R4.Pin_1
  N27: 7-9V.GND, 7-9V.GNDBREAK, PWR.pin1
  N28: FTDI.pin1, RST.pin2, C3.0
  N29: R4.Pin_0, LED1.cathode, ExtLED.pin1

notes:
  ECUv2.1 PROVOLT
