# Fritzing sketch id719_Traffic_Lights (saved by Fritzing 0.4.3b)
breadboards: 1

parts:
  Arduino1 = Arduino
  LEDG_|_Green = green LED - 5mm
  LEDA_|_Yellow_/_Amber = yellow LED - 5mm
  LEDR_|_Red = Red LED - 5mm
  WAIT = yellow LED - 5mm
  WALK = white LED - 5mm
  S1 = Pushbutton [package="[THT]"]
  R2 = Resistor [resistance=10k package=THT]
  R1 = Trimmer Potentiometer [package=THT]

nets:
  N1: Arduino1.GND, LEDG_|_Green.cathode, LEDA_|_Yellow_/_Amber.cathode, LEDR_|_Red.cathode, WAIT.cathode, WALK.cathode, R2.Pin_1, R1.leg1
  N2: Arduino1.D11, LEDG_|_Green.anode
  N3: Arduino1.D10, LEDA_|_Yellow_/_Amber.anode
  N4: Arduino1.D9, LEDR_|_Red.anode
  N5: Arduino1.D7, S1.Pin_1, S1.Pin_2, R2.Pin_0
  N6: Arduino1.D4, WAIT.anode
  N7: Arduino1.D3, WALK.anode
  N8: Arduino1.+5V, S1.Pin_3, S1.Pin_4, R1.leg2
  N9: Arduino1.A2, R1.wiper
