# Fritzing sketch id720_AVR_0 (saved by Fritzing 0.9.3b)
breadboards: 1

parts:
  R1 = Resistor [tolerance=±5% resistance=10k package="0402 [SMD]"]
  Y1 = CRYSTAL [package=crystal-smd-10.5x4.8-2pin]
  C1 = Capacitor [package=cap-pth-small2]
  C2 = Capacitor [package=cap-pth-small2]
  J1 = AVR ISP 6 Pin [package=2x3-ns]
  U1 = atmega328 [package=dip]

nets:
  N1: R1.Pin_0, J1.2, U1.VCC
  N2: R1.Pin_1, J1.5, U1.RESET
  N3: Y1.1, C1.1, U1.XLAT2
  N4: Y1.2, C2.1, U1.XLAT1
  N5: C1.2, C2.2, J1.6, U1.GND#7
  N6: J1.1, U1.D12
  N7: J1.3, U1.D13
  N8: J1.4, U1.D11_(PWM)
