# Fritzing sketch id721_9_grid_charlieplex_0 (saved by Fritzing 0.9.3b)
circuit board: 5.36386cm x 2.31066cm
breadboards: 1

parts:
  L2 = LED - 3mm [color="Red (633nm)" package="3 mm [THT]"]
  L1 = LED - 3mm [color="Red (633nm)" package="3 mm [THT]"]
  L0 = LED - 3mm [color="Red (633nm)" package="3 mm [THT]"]
  L3 = LED - 3mm [color="Red (633nm)" package="3 mm [THT]"]
  L4 = LED - 3mm [color="Red (633nm)" package="3 mm [THT]"]
  L6 = LED - 3mm [color="Red (633nm)" package="3 mm [THT]"]
  L8 = LED - 3mm [color="Red (633nm)" package="3 mm [THT]"]
  L7 = LED - 3mm [color="Red (633nm)" package="3 mm [THT]"]
  L5 = LED - 3mm [color="Red (633nm)" package="3 mm [THT]"]
  R2 = Resistor [tolerance=±5% resistance=220 package=THT]
  pow = female alternating pin header, 2 pins [form="♀ (female)"]
  R3 = Resistor [tolerance=±5% resistance=220 package=THT]
  R1 = Resistor [tolerance=±5% resistance=220 package=THT]
  R4 = Resistor [tolerance=±5% resistance=220 package=THT]
  att45 = ATTINY45 [part_number=attiny package=dip]
  prog = AVR ISP 6 Pin [package=2x3]

nets:
  N1: L2.cathode, L1.cathode, L0.cathode, R1.Pin_0, att45.PB1(MISO), prog.1
  N2: L2.anode, L8.anode, L5.anode, R4.Pin_1
  N3: L1.anode, L4.anode, R3.Pin_1
  N4: L0.anode, L7.anode, R2.Pin_1
  N5: L3.cathode, L4.cathode, L5.cathode, R2.Pin_0, att45.PB0(MOSI), prog.4
  N6: L3.anode, L6.anode, R1.Pin_1
  N7: L6.cathode, L8.cathode, L7.cathode, R3.Pin_0, att45.PB2(SCK_ADC1), prog.3
  N8: pow.pin1, att45.GND, prog.6
  N9: pow.pin2, att45.VCC, prog.2
  N10: R4.Pin_0, att45.PB3(ADC3)

notes:
  + -
  Created: by codehunger www.codehunger.com
