# Fritzing sketch id723_Attiny85_work_horse_board_0 (saved by Fritzing 0.9.1b)
circuit board: 4.5cm x 4cm
breadboards: 1

parts:
  5v = attiny85 [package=dip]
  3 = Screw terminal - 2 pins [package=THT]
  1 = Screw terminal - 2 pins [package=THT]
  4 = Screw terminal - 2 pins [package=THT]
  gnd = Screw terminal - 2 pins [package=THT]
  5v_Out = Screw terminal - 2 pins [package=THT]
  LED1 = LED - 5mm [color="Red (633nm)" package="5 mm [THT]"]
  0 = Resistor [tolerance=±5% resistance=220 package=THT]
  2 = female pin header, 4 pins [form="♀ (female)"]
  Reset = SWITCH-MOMENTARY-2 [package=tactile-pth]
  J2 = female pin header, 2 pins [form="♀ (female)"]
  J3 = female pin header, 2 pins [form="♀ (female)"]
  R = female pin header, 4 pins [form="♀ (female)"]
  C1 = Electrolytic Capacitor [capacitance=100nF voltage=35V package="100 mil [THT, electrolytic]"]
  C2 = Electrolytic Capacitor [capacitance=100nF voltage=35V package="100 mil [THT, electrolytic]"]
  U1 = Voltage Regulator - 5V [package="TO220 [THT]"]
  gnd1 = Screw terminal - 2 pins [package=THT]
  J4 = female pin header, 2 pins [form="♀ (female)"]

nets:
  N1: 5v.Pin_1, 4.pin2, Reset.2, J2.pin1, R.pin1
  N2: 5v.Pin_2, 4.pin1, R.pin2
  N3: 5v.Pin_3, gnd.pin2, R.pin3
  N4: 5v.Pin_4, gnd.pin1, 5v_Out.pin1, LED1.cathode, Reset.1, J2.pin2, J3.pin2, R.pin4, C1.-, C2.-, U1.GND, gnd1.pin1, J4.pin2
  N5: 5v.Pin_5, 1.pin2, 0.Pin_0, 2.pin4
  N6: 5v.Pin_6, 1.pin1, 2.pin3
  N7: 5v.Pin_7, 3.pin2, 2.pin2
  N8: 5v.Pin_8, 3.pin1, 5v_Out.pin2, 2.pin1, J3.pin1, C2.+, U1.output_voltage
  N9: LED1.anode, 0.Pin_1
  N10: C1.+, U1.input_voltage, gnd1.pin2, J4.pin1

notes:
  -
  +
  Mi-Tec Design, LLC
  Rev A
  11/16/14
  5v out
  7-12v IN
  - +
  ATtiny 85
  Work Horse
  Arduino
  Compatible
