# Fritzing sketch id724_Untitled_Sketch_0 (saved by Fritzing 0.9.3b)
breadboards: 1

parts:
  Εξάρτημα1 = Breakout Board for Electret Microphone
  R1 = Resistor [tolerance=±5% resistance=220 package="0603 [SMD]"]
  R2 = Resistor [tolerance=±5% resistance=220 package="0603 [SMD]"]
  R3 = Resistor [tolerance=±5% resistance=220 package="0603 [SMD]"]
  LED1 = LED - 3mm [color="Blue (505nm)" package="3 mm [THT]"]
  LED2 = LED - 3mm [color="Blue (505nm)" package="3 mm [THT]"]
  LED3 = LED - 3mm [color="Blue (505nm)" package="3 mm [THT]"]
  R4 = Resistor [tolerance=±5% resistance=220 package="0603 [SMD]"]
  R5 = Resistor [tolerance=±5% resistance=220 package="0603 [SMD]"]
  R6 = Resistor [tolerance=±5% resistance=220 package="0603 [SMD]"]
  LED4 = LED - 3mm [color="Blue (505nm)" package="3 mm [THT]"]
  LED5 = LED - 3mm [color="Blue (505nm)" package="3 mm [THT]"]
  LED6 = LED - 3mm [color="Blue (505nm)" package="3 mm [THT]"]
  R7 = Resistor [tolerance=±5% resistance=220 package="0603 [SMD]"]
  LED7 = LED - 3mm [color="Red (633nm)" package="3 mm [THT]"]
  U1 = ATTINY13 [package=dip]

nets:
  VCC: Εξάρτημα1.VCC, U1.VCC
  GND: Εξάρτημα1.GND, LED1.cathode, LED2.cathode, LED3.cathode, LED4.cathode, LED5.cathode, LED6.cathode, LED7.cathode, U1.GND
  N1: Εξάρτημα1.AUD, U1.PB4(ADC2)
  N2: R1.Pin_0, R2.Pin_0, R3.Pin_0, U1.PB0(MOSI)
  N3: R1.Pin_1, R2.Pin_1, R3.Pin_1, LED1.anode, LED2.anode, LED3.anode
  N4: R4.Pin_0, R5.Pin_0, R6.Pin_0, U1.PB1(MISO)
  N5: R4.Pin_1, R5.Pin_1, R6.Pin_1, LED4.anode, LED5.anode, LED6.anode
  N6: R7.Pin_0, LED7.anode
  N7: R7.Pin_1, U1.PB2(SCK_ADC1)
