# Fritzing sketch id725_ATTiny_LEDs_0 (saved by Fritzing 0.9.0b)
circuit board: 7.9cm x 5.3cm
breadboards: 3

parts:
  74HC595 = 74HC595 [package="DIP16 [THT]"]
  ATTiny = attiny85 [package=dip]
  128 = LED - 5mm [color="Red (633nm)" package="5 mm [THT]"]
  64 = LED - 5mm [color="Red (633nm)" package="5 mm [THT]"]
  32 = LED - 5mm [color="Red (633nm)" package="5 mm [THT]"]
  16 = LED - 5mm [color="Red (633nm)" package="5 mm [THT]"]
  8 = LED - 5mm [color="Red (633nm)" package="5 mm [THT]"]
  4 = LED - 5mm [color="Red (633nm)" package="5 mm [THT]"]
  2 = LED - 5mm [color="Red (633nm)" package="5 mm [THT]"]
  1 = LED - 5mm [color="Red (633nm)" package="5 mm [THT]"]
  R1 = Resistor [tolerance=±5% resistance=220 package=THT]
  R2 = Resistor [tolerance=±5% resistance=220 package=THT]
  R3 = Resistor [tolerance=±5% resistance=220 package=THT]
  R4 = Resistor [tolerance=±5% resistance=220 package=THT]
  R5 = Resistor [tolerance=±5% resistance=220 package=THT]
  R6 = Resistor [tolerance=±5% resistance=220 package=THT]
  R7 = Resistor [tolerance=±5% resistance=220 package=THT]
  R8 = Resistor [tolerance=±5% resistance=220 package=THT]
  U3 = Voltage Regulator - 5V [package="TO220 [THT]"]
  U4 = mystery part, 3 pins [chip_label="Pin 0"]
  U5 = mystery part, 3 pins [chip_label="Pin 1"]
  U6 = mystery part, 3 pins [chip_label=Reset]
  VCC1 = Battery block 9V
  U7 = mystery part, 3 pins [chip_label=Serial]

nets:
  N1: 74HC595.Q1, R2.Pin_1
  N2: 74HC595.Q2, R3.Pin_1
  N3: 74HC595.Q3, R4.Pin_1
  N4: 74HC595.Q4, R5.Pin_1
  N5: 74HC595.Q5, R6.Pin_1
  N6: 74HC595.Q6, R7.Pin_1
  N7: 74HC595.Q7, R8.Pin_1
  GND: 74HC595.GND, 74HC595.OE, ATTiny.Pin_4, 128.cathode, 64.cathode, 32.cathode, 16.cathode, 8.cathode, 4.cathode, 2.cathode, 1.cathode, U3.GND, U4.pin1, U5.pin1, U6.pin1, VCC1.-, U7.pin1
  N8: 74HC595.Q7', U7.pin3
  N9: 74HC595.MR, 74HC595.VCC, ATTiny.Pin_8, U3.output_voltage, U4.pin2, U5.pin2, U6.pin2, U7.pin2
  N10: 74HC595.SH_CP, ATTiny.Pin_2
  N11: 74HC595.ST_CP, ATTiny.Pin_3
  N12: 74HC595.DS, ATTiny.Pin_7
  N13: 74HC595.Q0, R1.Pin_1
  N14: ATTiny.Pin_1, U6.pin3
  N15: ATTiny.Pin_5, U4.pin3
  N16: ATTiny.Pin_6, U5.pin3
  N17: 128.anode, R8.Pin_0
  N18: 64.anode, R7.Pin_0
  N19: 32.anode, R6.Pin_0
  N20: 16.anode, R5.Pin_0
  N21: 8.anode, R4.Pin_0
  N22: 4.anode, R3.Pin_0
  N23: 2.anode, R2.Pin_0
  N24: 1.anode, R1.Pin_0
  N25: U3.input_voltage, VCC1.+

notes:
  Knowledge And Technology Joyfully Engaged
  W.A. ten Brink
  Pin 0
  Pin 1
  VCC
  Ground
  Data
  Reset
  Serial
  9 volt in
  5 volt out
  MSB
  LSB
  Resistor
