# Fritzing sketch id726_ATTinyTraining_0 (saved by Fritzing 0.7.5b)
breadboards: 1

parts:
  IC1 = IC, DIP package, 14 pins [chip_label=ATTiny24/44/84 spacing=300mil]
  J2 = female pin header, 7 pins [form="♀ (female)"]
  J3 = female pin header, 7 pins [form="♀ (female)"]
  J1 = shrouded pin header, 6 pins [form="♂ (shrouded male)"]
  R1 = Resistor [tolerance=±5% resistance=220 package=THT]
  R2 = Resistor [tolerance=±5% resistance=220 package=THT]
  R3 = Resistor [tolerance=±5% resistance=220 package=THT]
  R4 = Resistor [tolerance=±5% resistance=220 package=THT]
  S1 = Pushbutton [package=THT]
  S2 = Pushbutton [package=THT]
  S3 = Pushbutton [package=THT]
  S4 = Pushbutton [package=THT]
  R5 = Resistor [tolerance=±5% resistance=10k package=THT]
  R6 = Resistor [tolerance=±5% resistance=10k package=THT]
  R7 = Resistor [tolerance=±5% resistance=10k package=THT]
  R8 = Resistor [tolerance=±5% resistance=10k package=THT]
  LED1 = LED - 3mm [color="Red (633nm)" package="3 mm [THT]"]
  LED2 = LED - 3mm [color="Red (633nm)" package="3 mm [THT]"]
  LED4 = LED - 3mm [color="Red (633nm)" package="3 mm [THT]"]
  LED3 = LED - 3mm [color="Red (633nm)" package="3 mm [THT]"]
  J6 = female pin header, 3 pins [form="♀ (female)"]
  IC2 = 24LC16 [package=THT]
  Power_plug1 = Power plug
  U1 = Voltage Regulator - 5V [package="TO220 [THT]"]
  J8 = female pin header, 6 pins [form="♀ (female)"]
  J7 = female pin header, 6 pins [form="♀ (female)"]
  7_Segment1 = 7 Segment Display
  R9 = Temperature Sensor (Thermistor) [thermistor_type=NTC package=THT]
  R10 = Trimmer Potentiometer [maximum_resistance=10kΩ package=THT]
  R11 = Photocell (LDR) [package=THT]
  R12 = Trimmer Potentiometer [maximum_resistance=10kΩ package=THT]
  J11 = female pin header, 4 pins [form="♀ (female)"]
  IC3 = IC, DIP package, 16 pins [chip_label=LCD-CD4056BE spacing=300mil]
  J9 = female pin header, 5 pins [form="♀ (female)"]
  J5 = female pin header, 5 pins [form="♀ (female)"]
  S5 = Pushbutton [package=THT]
  J4 = female pin header, 5 pins [form="♀ (female)"]
  LED5 = LED - 3mm [color="Red (633nm)" package="3 mm [THT]"]
  R14 = Resistor [tolerance=±5% resistance=220 package=THT]
  R15 = Resistor [tolerance=±5% resistance=10k package=THT]
  J13 = female pin header, 3 pins [form="♀ (female)"]
  J12 = screw terminal, 3 pins

nets:
  5V: IC1.pin1, J2.pin7, J1.pin6, S1.leg1, S2.leg1, S3.leg1, S4.leg1, IC2.+V, U1.output_voltage, J8.pin1, J8.pin2, J8.pin3, J8.pin4, J8.pin5, J8.pin6, R9.pin_0, R10.leg1, R11.pin_1, R12.leg1, IC3.pin16, S5.leg1
  N1: IC1.pin2, J2.pin6
  N2: IC1.pin3, J2.pin5
  N3: IC1.pin4, J2.pin4, J1.pin3
  N4: IC1.pin5, J2.pin3
  N5: IC1.pin6, J2.pin2
  N6: IC1.pin7, J2.pin1, J1.pin5
  N7: IC1.pin8, J3.pin7, J1.pin1
  N8: IC1.pin9, J3.pin6, J1.pin2
  N9: IC1.pin10, J3.pin5
  N10: IC1.pin11, J3.pin4
  N11: IC1.pin12, J3.pin3
  N12: IC1.pin13, J3.pin2
  GND: IC1.pin14, J3.pin1, J1.pin4, R1.Pin_0, R2.Pin_0, R3.Pin_0, R4.Pin_0, R5.Pin_0, R6.Pin_0, R7.Pin_0, R8.Pin_0, IC2.A0, IC2.A1, IC2.A2, IC2.0V, Power_plug1.GND, U1.GND, J7.pin1, J7.pin2, J7.pin3, J7.pin4, J7.pin5, J7.pin6, 7_Segment1.common_cathode, R10.leg2, R12.leg2, IC3.pin6, IC3.pin7, IC3.pin8, R14.Pin_0, R15.Pin_0
  N13: R1.Pin_1, LED1.cathode
  N14: R2.Pin_1, LED2.cathode
  N15: R3.Pin_1, LED3.cathode
  N16: R4.Pin_1, LED4.cathode
  N17: S1.leg0, R8.Pin_1, J5.pin1
  N18: S2.leg0, R6.Pin_1, J5.pin2
  N19: S3.leg0, R5.Pin_1, J5.pin3
  N20: S4.leg0, R7.Pin_1, J5.pin4
  N21: LED1.anode, J4.pin1
  N22: LED2.anode, J4.pin2
  N23: LED4.anode, J4.pin4
  N24: LED3.anode, J4.pin3
  N25: J6.pin1, IC2.WP_-_Write_Protect
  N26: J6.pin2, IC2.SCL_-_I2C_Clock
  N27: J6.pin3, IC2.SDA_-_I2C_Data
  N28: Power_plug1.VCC, U1.input_voltage
  N29: 7_Segment1.Segment_A#1, IC3.pin14
  N30: 7_Segment1.Segment_F, IC3.pin15
  N31: 7_Segment1.Segment_E, IC3.pin13
  N32: 7_Segment1.Segment_D, IC3.pin12
  N33: 7_Segment1.Segment_C, IC3.pin11
  N34: 7_Segment1.Segment_B, IC3.pin10
  N35: 7_Segment1.Segment_A#10, IC3.pin9
  N36: R9.pin_1, J11.pin3
  N37: R10.wiper, J11.pin1
  N38: R11.pin_0, J11.pin2
  N39: R12.wiper, J11.pin4
  N40: IC3.pin1, J9.pin5
  N41: IC3.pin2, J9.pin2
  N42: IC3.pin3, J9.pin3
  N43: IC3.pin4, J9.pin1
  N44: IC3.pin5, J9.pin4
  N45: J5.pin5, S5.leg0, R15.Pin_1
  N46: J4.pin5, LED5.anode
  N47: LED5.cathode, R14.Pin_1
  N48: J13.pin1, J12.pin1
  N49: J13.pin2, J12.pin2
  N50: J13.pin3, J12.pin3

notes:
  ATTiny84
  Trainer
