# Fritzing sketch id727_attiny45breakout_R2_0 (saved by Fritzing 0.7.4b)

parts:
  Power_plug1 = Power plug
  7805 = Voltage Regulator - 5V [package="TO220 [THT]"]
  J_L = male pin header, 4 pins [form="♂ (male)"]
  J_R = male pin header, 4 pins [form="♂ (male)"]
  Ci = Ceramic Capacitor [capacitance=330nF package="1206 [SMD, multilayer]"]
  Co = Ceramic Capacitor [capacitance=100nF package="1206 [SMD, multilayer]"]
  POW = female pin header, 2 pins [form="♀ (female)"]
  Rr = Resistor [tolerance=±5% resistance=10k package="1206 [SMD]"]
  RESET = Pushbutton [package="[THT]"]
  ATTINY25/45/85 = ATtiny35_45_85
  ICSP = Generic_shrouded_header___10_pins [form="♂ (shrouded male)"]

nets:
  GND: Power_plug1.GND, 7805.GND, J_L.pin1, Ci.0, Co.0, POW.pin1, RESET.Pin_1, RESET.Pin_2, ATTINY25/45/85.connector3, ICSP.connector1, ICSP.connector5, ICSP.connector6, ICSP.connector7, ICSP.connector8
  N1: Power_plug1.VCC, 7805.input_voltage, Ci.1
  5V: 7805.output_voltage, J_R.pin1, Co.1, POW.pin2, Rr.Pin_0, ATTINY25/45/85.connector7, ICSP.connector9
  N2: J_L.pin2, ATTINY25/45/85.connector2
  N3: J_L.pin3, ATTINY25/45/85.connector1
  N4: J_L.pin4, Rr.Pin_1, RESET.Pin_3, RESET.Pin_4, ATTINY25/45/85.connector0, ICSP.connector2
  N5: J_R.pin2, ATTINY25/45/85.connector6, ICSP.connector3
  N6: J_R.pin3, ATTINY25/45/85.connector5, ICSP.connector4
  N7: J_R.pin4, ATTINY25/45/85.connector4, ICSP.connector0

notes:
  5V
  GND
