# Fritzing sketch id728_ATTiny45ICSP_0 (saved by Fritzing 0.8.7b)
circuit board: 2.66142cm x 1.61508cm
perfboards: 1

parts:
  ICSP = male pin header, 3 pins [form="♂ (male)"]
  J2 = male pin header, 3 pins [form="♂ (male)"]
  ATTiny45/85 = ATTINY45 [package=dip]

nets:
  N1: ICSP.pin1, ATTiny45/85.GND
  N2: ICSP.pin2, ATTiny45/85.PB0(MOSI)
  N3: ICSP.pin3, ATTiny45/85.VCC
  N4: J2.pin1, ATTiny45/85.PB5(NRES)
  N5: J2.pin2, ATTiny45/85.PB2(SCK_ADC1)
  N6: J2.pin3, ATTiny45/85.PB1(MISO)

notes:
  GND
  +
