# Fritzing sketch id729_attiny_optiboot_0 (saved by Fritzing 0.8.5b)
breadboards: 1

parts:
  Bauteil1 = FTDI Basic Programmer
  U1 = attiny85 [package=dip]
  C1 = Ceramic Capacitor [capacitance=100nF package="100 mil [THT, multilayer]"]
  R1 = Resistor [tolerance=±5% resistance=220 package=THT]
  LED1 = LED - 5mm [color="Red (633nm)" package="5 mm [THT]"]
  R2 = Resistor [tolerance=±5% resistance=10k package=THT]
  C2 = Ceramic Capacitor [capacitance=100nF package="100 mil [THT, multilayer]"]

nets:
  N1: Bauteil1.DTR, C2.1
  N2: Bauteil1.RXI, U1.Pin_5
  N3: Bauteil1.TXO, U1.Pin_6
  N4: Bauteil1.POWER, U1.Pin_8, C1.1, R2.Pin_0
  N5: Bauteil1.GND, U1.Pin_4, C1.0
  N6: U1.Pin_1, R2.Pin_1, C2.0
  N7: U1.Pin_7, LED1.anode
  N8: R1.Pin_0, LED1.cathode
