# Fritzing sketch id730_ISP_ATtiny44_0 (saved by Fritzing 0.9.3b)
circuit board: 8.46667cm x 5.64444cm
breadboards: 1

parts:
  Componente1 = Arduino Nano (Rev3.0)
  Componente2 = attiny44
  LED1 = LED - 5mm [color="Red (633nm)" package="5 mm [THT]"]
  R1 = Resistor [tolerance=±5% resistance=100 package=THT]
  C1 = Electrolytic Capacitor [capacitance=1µF package="100 mil [THT, electrolytic]"]

nets:
  N1: Componente1.RESET, C1.+
  N2: Componente1.GND, Componente2.connector13, R1.Pin_0, C1.-
  N3: Componente1.D10, Componente2.connector3
  N4: Componente1.D11/MOSI, Componente2.connector6
  N5: Componente1.D12/MISO, Componente2.connector7
  N6: Componente1.5V, Componente2.connector0
  N7: Componente1.D13/SCK, Componente2.connector8
  N8: Componente2.connector1, LED1.anode
  N9: LED1.cathode, R1.Pin_1
