# Fritzing sketch id731_attiny85AutoOff1Pin_0 (saved by Fritzing 0.9.3b)
circuit board: 4.44176cm x 3.60024cm
breadboards: 1

parts:
  VCC1 = 4 x AAA Battery Mount
  R3 = Resistor [tolerance=±5% resistance=100k package=THT]
  R2 = Resistor [tolerance=±5% resistance=100k package=THT]
  R4 = Resistor [tolerance=±5% resistance=50k package=THT]
  S1_ON = Pushbutton [package="[THT]"]
  U2 = attiny85 [package=dip]
  Q1_BC547C_NPN = NPN-Transistor [package="TO92 [THT]"]
  Q2_BC557C_PNP = PNP-Transistor [package="TO92 [THT]"]
  R1 = Resistor [tolerance=±5% resistance=100k package=THT]
  LED1 = LED - 5mm [color="Red (633nm)" package="5 mm [THT]"]
  R5 = Resistor [tolerance=±5% resistance=100k package=THT]
  R6 = Resistor [tolerance=±5% resistance=100k package=THT]
  LED2 = LED - 5mm [color="White (4500K)" package="5 mm [THT]"]
  R7 = Resistor [tolerance=±5% resistance=1k package=THT]

nets:
  GND: VCC1.-, R4.Pin_0, U2.Pin_4, Q1_BC547C_NPN.E, R6.Pin_1, LED2.cathode
  N1: VCC1.+, R2.Pin_0, Q2_BC557C_PNP.E, R7.Pin_0
  N2: R3.Pin_0, Q2_BC557C_PNP.B
  N3: R3.Pin_1, R2.Pin_1, Q1_BC547C_NPN.C
  N4: R4.Pin_1, S1_ON.Pin_3, S1_ON.Pin_4, U2.Pin_2, R1.Pin_1
  N5: S1_ON.Pin_1, S1_ON.Pin_2, R7.Pin_1
  N6: U2.Pin_3, R5.Pin_1
  N7: U2.Pin_8, Q2_BC557C_PNP.C, LED1.anode
  N8: Q1_BC547C_NPN.B, R1.Pin_0
  N9: LED1.cathode, R6.Pin_0
  N10: R5.Pin_0, LED2.anode

notes:
  V+
  GND
  SCL
  SDA
  KEEP ON / READ BUTTON
  Custom LED (Optional)
