# Fritzing sketch id733_PIR_LED_Driver_0 (saved by Fritzing 0.8.7b)
circuit board: 2.99279cm x 1.55843cm

parts:
  C2 = Capacitor [package=cap-pth-small2]
  Q1 = Basic FET P-Channel [package="TO220 [THT]"]
  J2 = female pin header, 3 pins [form="♀ (female)"]
  R1 = Resistor [tolerance=±5% resistance=1k package=THT]
  C1 = Capacitor [package=cap-pth-small2]
  U2 = attiny85 [package=dip]
  IC1 = Voltage Regulator [package=to-92]
  JP2 = Header 4 [package=screwterminal-3.5mm-4_lock]
  D1 = Diode [package=diode-1n4148]
  R2 = Resistor [tolerance=±5% resistance=2.2k package=THT]
  LED1 = LED - 3mm [color="Red (633nm)" package="3 mm [THT]"]

nets (from the pcb view):
  N1: C2.1, J2.pin1, U2.Pin_8, IC1.OUT
  N2: C2.2, Q1.source, J2.pin2, C1.2, U2.Pin_4, IC1.GND, JP2.1, JP2.4, LED1.cathode
  N3: Q1.gate, R1.Pin_0
  N4: J2.pin3, U2.Pin_3
  N5: R1.Pin_1, U2.Pin_6
  N6: C1.1, IC1.IN, D1.C
  N7: U2.Pin_2, R2.Pin_1
  N8: JP2.2, JP2.3, D1.A
  N9: R2.Pin_0, LED1.anode
