# Fritzing sketch id734_ArduinoISP_attiny85_nano_0 (saved by Fritzing 0.7.11b)
breadboards: 1

parts:
  C1 = Electrolytic Capacitor [capacitance=1µF package="100 mil [THT, electrolytic]"]
  attiny = IC, DIP package, 8 pins [chip_label=IC]
  Arduino_UNO = Arduino Nano v3.0
  LED1 = LED - 5mm [color="Red (633nm)" package="5 mm [THT]"]
  R1 = Resistor [tolerance=±5% resistance=220 package=THT]

nets:
  N1: C1.-, attiny.pin4, Arduino_UNO.GND, LED1.cathode
  N2: C1.+, Arduino_UNO.RST
  N3: attiny.pin1, Arduino_UNO.D10
  N4: attiny.pin2, R1.Pin_0
  N5: attiny.pin5, Arduino_UNO.D11
  N6: attiny.pin6, Arduino_UNO.D12
  N7: attiny.pin7, Arduino_UNO.D13
  N8: attiny.pin8, Arduino_UNO.+5V
  N9: LED1.anode, R1.Pin_1
