# Fritzing sketch id735_ArduinoISP_attiny85_0 (saved by Fritzing 0.7.11b)
breadboards: 1

parts:
  Arduino_UNO = Arduino
  C1 = Electrolytic Capacitor [capacitance=1µF package="100 mil [THT, electrolytic]"]
  attiny = IC, DIP package, 8 pins [chip_label=IC]
  LED2 = LED - 5mm [color="Red (633nm)" package="5 mm [THT]"]
  R2 = Resistor [tolerance=±5% resistance=220 package=THT]

nets:
  N1: Arduino_UNO.GND, C1.-, attiny.pin4, LED2.cathode
  N2: Arduino_UNO.D13, attiny.pin7
  N3: Arduino_UNO.D12, attiny.pin6
  N4: Arduino_UNO.D11, attiny.pin5
  N5: Arduino_UNO.D10, attiny.pin1
  N6: Arduino_UNO.RST, C1.+
  N7: Arduino_UNO.+5V, attiny.pin8
  N8: attiny.pin3, R2.Pin_0
  N9: LED2.anode, R2.Pin_1
