# Fritzing sketch id736_USBtinyISP_ATtiny85_0 (saved by Fritzing 0.7.4b)
breadboards: 1

parts:
  U1 = attiny85 [package=dip]
  USBtinyISP1 = Generic_shrouded_header___6_pins [form="♂ (shrouded male)"]

nets:
  N1: U1.Pin_1, USBtinyISP1.connector2
  N2: U1.Pin_4, USBtinyISP1.connector3
  N3: U1.Pin_5, USBtinyISP1.connector4
  N4: U1.Pin_6, USBtinyISP1.connector0
  N5: U1.Pin_7, USBtinyISP1.connector1
  N6: U1.Pin_8, USBtinyISP1.connector5
