# Fritzing sketch id738_distance_sensor_v1_0 (saved by Fritzing 0.9.2b)
breadboards: 1

parts:
  U1 = attiny85 [package=dip]
  J1 = Piezo Speaker
  U2 = TRANSISTOR_NPN_2 [package=to-92]
  R1 = Resistor [tolerance=±5% resistance=10k package="0603 [SMD]"]
  D1 = Rectifier Diode [part_number=1N4001 package="300 mil [THT]"]
  BAT1 = Battery Holders [package=battcom_20mm_pth]
  Part1 = SRF05 Ultrasonic Rangefinder
  U3 = POT [package=pot_mammoth]
  U4 = POT [package=pot_mammoth]
  S1 = Pushbutton [package="[THT]"]
  LED1 = smd LED [color="Red (633nm)" package="0805 [SMD]"]

nets:
  N1: U1.Pin_2, U4.S
  N2: U1.Pin_3, U3.S
  N3: U1.Pin_5, R1.Pin_1
  N4: U1.Pin_6, Part1.connector9
  N5: U1.Pin_7, Part1.connector10
  N6: U1.Pin_8, S1.Pin_3, S1.Pin_4
  N7: J1.pin1, BAT1.+, Part1.connector11, U3.E, U4.E
  N8: J1.pin2, U2.E
  N9: U2.C, D1.anode, BAT1.-, Part1.connector8, U3.A, U4.A
  N10: U2.B, R1.Pin_0, LED1.anode
  N11: D1.cathode, S1.Pin_1, S1.Pin_2
  GND: LED1.cathode
