# Fritzing sketch id739_audi_a3_8p_Daylight_running_lights_sensor_switch_0 (saved by Fritzing 0.9.3b)
breadboards: 1

parts:
  R1 = PHOTOCELL [package=photocell-kit]
  R2 = Resistor [tolerance=±5% resistance=1.5k package="0603 [SMD]"]
  R3 = Trimmer Potentiometer [maximum_resistance=10kΩ package=THT]  # not connected
  Part1 = Arduino Nano (Rev3.0)
  IC1 = Voltage Regulator [package=to-220-alt]  # not connected
  LED1 = LED - 3mm [color="Red (633nm)" package="3 mm [THT]"]  # not connected
  LED2 = LED - 3mm [color="Red (633nm)" package="3 mm [THT]"]  # not connected
  R6 = Resistor [tolerance=±5% resistance=3.3k package="0603 [SMD]"]
  R7 = Resistor [tolerance=±5% resistance=390 package="0603 [SMD]"]  # not connected
  R8 = Resistor [tolerance=±5% resistance=390 package="0603 [SMD]"]  # not connected
  Q1 = TRANSISTOR_PNP [package=to-92]
  R9 = Resistor [tolerance=±5% resistance=8.2k package="0603 [SMD]"]
  R10 = Resistor [tolerance=±5% resistance=390 package="0603 [SMD]"]
  R11 = Resistor [tolerance=±5% resistance=390 package="0603 [SMD]"]
  Q2 = TRANSISTOR_PNP [package=to-92]
  U1 = RELAY [package=relay-g5q]
  U2 = RELAY [package=relay-g5q]
  D1 = Zener Diode [part_number=1N4732A breakdown_voltage=3.6V package="300 mil [THT]"]
  D2 = Zener Diode [part_number=1N4732A breakdown_voltage=3.6V package="300 mil [THT]"]
  SW1 = ENCODER_RGB_CA [package=encoder_led_3]

nets:
  N1: R1.P$1, Part1.5V
  N2: R1.P$2, R2.Pin_1
  N3: Part1.GND, Q1.E
  N4: Part1.D5, R10.Pin_1
  N5: Part1.D6, R11.Pin_1
  N6: Part1.D8, R6.Pin_0
  N7: R6.Pin_1, R9.Pin_0
  N8: Q1.B, R10.Pin_0
  N9: Q1.C, U1.COIL1, D2.anode
  N10: R9.Pin_1, Q2.E
  N11: R11.Pin_0, Q2.B
  N12: Q2.C, U2.COIL2, D1.anode
  N13: U1.COIL2, U1.MAIN, U2.COIL1, D1.cathode, D2.cathode
  N14: U2.MAIN, SW1.C

notes:
  Pin1 from switch (Low Beam ON->"GND")
  Car  GND +12V
  Pin 1 default Connected (Low-Beam Off, Switch 0-position)
  Pin 1 default Connected (Low-Beam Off)
  car ecu
  Pin 9
  Pin 1 < "open" -> ECU (Low-Beam ON)
  DLR leds ON
  Light Switch manually in Low-beam -> DLR off
  DayTime Running Lights
  Led bar next to fog lights
