# Fritzing sketch id746_mode_button_emulator_0 (saved by Fritzing 0.8.3b)
circuit board: 1.25735cm x 1.36056cm
breadboards: 1

parts:
  R1 = Resistor [tolerance=±5% resistance=10k package="1206 [SMD]"]
  R2 = Resistor [tolerance=±5% resistance=10k package="1206 [SMD]"]
  U1 = ATTINY45 [package=so]
  J1 = longpad pin header, 5 pins [form="long pad"]

nets:
  N1: R1.Pin_0, U1.PB5(NRES)
  N2: R1.Pin_1, R2.Pin_1, U1.VCC, J1.pin2
  N3: R2.Pin_0, U1.PB0(MOSI), J1.pin4
  N4: U1.GND, J1.pin1
  N5: U1.PB1(MISO), J1.pin3
  N6: U1.PB2(SCK_ADC1), J1.pin5

notes:
  GND      Remote(FB)      LED
  +5V       BUTTON
