# Fritzing sketch id747_SMD_0 (saved by Fritzing 0.8.3b)
circuit board: 3.11715cm x 1.4168cm
circuit board: 2.7184cm x 1.44746cm
perfboards: 2

parts:
  radio1 = longpad pin header, 5 pins [form="long pad"]
  radio2 = longpad pin header, 5 pins [form="long pad"]
  U4 = Voltage Regulator - 5V [package="DPak [SMD]"]
  IC2 = SO08 [chip_label=IC package=SO]
  IC3 = SO08 [chip_label=IC package=SO]
  U3 = Voltage Regulator - 5V [package="DPak [SMD]"]
  R49 = Resistor [tolerance=±5% resistance=3.3k package="1206 [SMD]"]
  R47 = Resistor [tolerance=±5% resistance=3.3k package="1206 [SMD]"]
  R48 = Resistor [tolerance=±5% resistance=3.3k package="1206 [SMD]"]
  R48_2 = Resistor [tolerance=±5% resistance=10k package="1206 [SMD]"]
  C15 = Ceramic Capacitor [capacitance=100nF voltage=20V package="1206 [SMD, multilayer]"]
  C14 = Ceramic Capacitor [capacitance=100nF voltage=20V package="1206 [SMD, multilayer]"]
  R52 = Resistor [tolerance=±5% resistance=3.3k package="1206 [SMD]"]
  R51 = Resistor [tolerance=±5% resistance=3.3k package="1206 [SMD]"]
  R50 = Resistor [tolerance=±5% resistance=3.3k package="1206 [SMD]"]
  C16 = Ceramic Capacitor [capacitance=100nF voltage=20V package="1206 [SMD, multilayer]"]
  C17 = Ceramic Capacitor [capacitance=100nF voltage=20V package="1206 [SMD, multilayer]"]
  R53 = Resistor [tolerance=±5% resistance=10k package="1206 [SMD]"]

nets:
  N1: radio1.pin1, U3.input_voltage, C14.1
  N2: radio1.pin2, IC3.8, U3.GND, C15.0, C14.0
  N3: radio1.pin3, R49.Pin_0
  N4: radio1.pin4, R47.Pin_0
  N5: radio1.pin5, R48.Pin_0
  N6: radio2.pin1, U4.GND, IC2.8, C16.0, C17.0
  N7: radio2.pin2, U4.input_voltage, C16.1
  N8: radio2.pin3, R51.Pin_0
  N9: radio2.pin4, R50.Pin_0
  N10: radio2.pin5, R52.Pin_0
  N11: U4.output_voltage, IC2.1, C17.1, R53.Pin_0
  N12: IC2.2, R50.Pin_1
  N13: IC2.3, R51.Pin_1
  N14: IC2.4, R53.Pin_1
  N15: IC2.5, R52.Pin_1
  N16: IC3.1, U3.output_voltage, R48_2.Pin_0, C15.1
  N17: IC3.4, R48_2.Pin_1
  N18: IC3.5, R49.Pin_1
  N19: IC3.6, R47.Pin_1
  N20: IC3.7, R48.Pin_1

notes:
  V2
  gnd
  DO
  CLK
  DI
  +12V
