# Fritzing sketch id748_THT_0 (saved by Fritzing 0.8.3b)
circuit board: 3.84932cm x 1.56109cm
circuit board: 3.87602cm x 1.6363cm
perfboards: 2

parts:
  radio1 = longpad pin header, 5 pins [form="long pad"]
  U3 = Voltage Regulator - 5V [package="TO220 [THT]"]
  R49 = Resistor [tolerance=±5% resistance=3.3k package=THT]
  R47 = Resistor [tolerance=±5% resistance=3.3k package=THT]
  R48 = Resistor [tolerance=±5% resistance=3.3k package=THT]
  IC1 = IC, DIP package, 8 pins [chip_label=IC]
  R48_2 = Resistor [tolerance=±5% resistance=10k package=THT]
  R50 = Resistor [tolerance=±5% resistance=3.3k package=THT]
  R51 = Resistor [tolerance=±5% resistance=3.3k package=THT]
  R52 = Resistor [tolerance=±5% resistance=3.3k package=THT]
  R53 = Resistor [tolerance=±5% resistance=10k package=THT]
  radio2 = longpad pin header, 5 pins [form="long pad"]
  U4 = Voltage Regulator - 5V [package="TO220 [THT]"]
  IC2 = IC, DIP package, 8 pins [chip_label=IC]
  C16 = Ceramic Capacitor [capacitance=100nF voltage=20V package="200 mil [THT, multilayer]"]
  C17 = Ceramic Capacitor [capacitance=100nF voltage=20V package="200 mil [THT, multilayer]"]
  C14 = Ceramic Capacitor [capacitance=100nF voltage=20V package="200 mil [THT, multilayer]"]
  C15 = Ceramic Capacitor [capacitance=100nF voltage=20V package="200 mil [THT, multilayer]"]

nets:
  N1: radio1.pin1, U3.input_voltage, C14.1
  N2: radio1.pin2, U3.GND, IC1.pin8, C14.0, C15.0
  N3: radio1.pin3, R48.Pin_0
  N4: radio1.pin4, R47.Pin_0
  N5: radio1.pin5, R49.Pin_0
  N6: U3.output_voltage, IC1.pin1, R48_2.Pin_0, C15.1
  N7: R49.Pin_1, IC1.pin5
  N8: R47.Pin_1, IC1.pin6
  N9: R48.Pin_1, IC1.pin7
  N10: IC1.pin4, R48_2.Pin_1
  N11: R50.Pin_0, radio2.pin3
  N12: R50.Pin_1, IC2.pin2
  N13: R51.Pin_0, radio2.pin4
  N14: R51.Pin_1, IC2.pin3
  N15: R52.Pin_0, radio2.pin5
  N16: R52.Pin_1, IC2.pin5
  N17: R53.Pin_0, U4.output_voltage, IC2.pin1, C17.1
  N18: R53.Pin_1, IC2.pin4
  N19: radio2.pin1, U4.GND, IC2.pin8, C16.0, C17.0
  N20: radio2.pin2, U4.input_voltage, C16.1

notes:
  V2
  +12V
  gnd
  DO
  CLK
  DI
