# Fritzing sketch id749_denne_Svietenie_0 (saved by Fritzing 0.7.12b)
breadboards: 1

parts:
  Q1 = Basic FET P-Channel [part_number=IRF9630 package="TO220 [THT]"]
  Q2 = Basic FET P-Channel [part_number=IRF9630 package="TO220 [THT]"]
  Q3 = Basic FET P-Channel [part_number=IRF9630 package="TO220 [THT]"]
  J1 = screw terminal, 6 pins [part_number=ARK300V]
  R1 = Resistor [tolerance=±5% resistance=220 package="1206 [SMD]"]
  R2 = Resistor [tolerance=±5% resistance=220 package="1206 [SMD]"]
  Q4 = NPN-Transistor [package="SOT-23 [SMD]"]

nets:
  N1: Q1.gate, Q2.gate, Q3.gate, R1.Pin_1, Q4.1
  N2: Q1.drain, Q2.drain, Q3.drain, J1.pin1, R1.Pin_0
  N3: Q1.source, J1.pin4
  N4: Q2.source, J1.pin5
  N5: Q3.source, J1.pin6
  N6: J1.pin2, R2.Pin_0
  N7: J1.pin3, Q4.2
  N8: R2.Pin_1, Q4.0

notes:
  o
  gnd
  on
  +12V
