# Fritzing sketch id750_denne_Svietenie_rele_0 (saved by Fritzing 0.7.12b)
breadboards: 1

parts:
  OMRON1 = OMRON PCB Power Relay – G5LE [part_number="G5LE-1 \n" package=THT]
  OMRON2 = OMRON PCB Power Relay – G5LE [part_number="G5LE-1 \n" package=THT]
  OMRON3 = OMRON PCB Power Relay – G5LE [part_number="G5LE-1 \n" package=THT]
  J1 = screw terminal, 6 pins

nets:
  N1: OMRON1.COIL1, OMRON2.COIL1, OMRON3.COIL1, J1.pin6
  N2: OMRON1.C, OMRON2.C, OMRON3.C, J1.pin3
  N3: OMRON1.COIL2, OMRON2.COIL2, OMRON3.COIL2, J1.pin2
  N4: OMRON1.B, J1.pin1
  N5: OMRON2.B, J1.pin5
  N6: OMRON3.B, J1.pin4
