# Fritzing sketch id752_denne_Svietenie_rele_D_stad_up_0 (saved by Fritzing 0.7.12b)
breadboards: 1

parts:
  J1 = screw terminal, 6 pins
  D2 = diode_1N4001_300mil.fzp [part_number=P1000K]
  D3 = diode_1N4001_300mil.fzp [part_number=P1000K]
  RELAY1 = CAR RELAY [part_number=NVF4-2 package=THT]
  D1 = diode_1N4001_300mil.fzp [part_number=P1000K]

nets:
  N1: J1.pin1, RELAY1.85
  N2: J1.pin2, RELAY1.87
  N3: J1.pin3, RELAY1.86
  N4: J1.pin4, D2.connector0
  N5: J1.pin5, D3.connector0
  N6: J1.pin6, D1.connector0
  N7: D2.connector1, D3.connector1, RELAY1.30, D1.connector1
