# Fritzing sketch id754_arduinolifx_video_breadboard (saved by Fritzing 0.9.3b)
breadboards: 1

parts:
  IC1 = ULN2003A [package="DIP16 [THT]"]
  LED1 = RGB LED (com. anode, rbg) [package="5 mm [THT]"]
  Part1 = Ethernet Pro

nets:
  N1: IC1.In_1, Part1.IO6
  N2: IC1.In_2, Part1.IO5
  N3: IC1.In_3, Part1.IO3
  GND: IC1.In_4, IC1.In_5, IC1.In_6, IC1.In_7, IC1.0V, Part1.GND
  N4: IC1.Out_3, LED1.red_cathode
  N5: IC1.Out_2, LED1.green_cathode
  N6: IC1.Out_1, LED1.blue_cathode
  12V: LED1.common_anode

notes:
  12V
  GND
