# Fritzing sketch id755_audio_chaser_PVlgTUH_0 (saved by Fritzing 0.9.3b)
circuit board: 5.03363cm x 5.60283cm
breadboards: 1

parts:
  Part1 = Breakout Board for Electret Microphone
  VCC1 = Battery block 9V
  R1 = Resistor [tolerance=±5% resistance=1k package=THT]
  LED1 = LED - 5mm [color="Red (633nm)" package="5 mm [THT]"]
  74HC1 = IC Johnson Decade 74HC4017 [chip_label=74HC4017]
  LED2 = LED - 5mm [color="Red (633nm)" package="5 mm [THT]"]
  LED3 = LED - 5mm [color="Red (633nm)" package="5 mm [THT]"]
  LED4 = LED - 5mm [color="Red (633nm)" package="5 mm [THT]"]
  LED5 = LED - 5mm [color="Red (633nm)" package="5 mm [THT]"]
  LED6 = LED - 5mm [color="Red (633nm)" package="5 mm [THT]"]
  LED7 = LED - 5mm [color="Red (633nm)" package="5 mm [THT]"]
  LED8 = LED - 5mm [color="Red (633nm)" package="5 mm [THT]"]
  LED10 = LED - 5mm [color="Red (633nm)" package="5 mm [THT]"]
  LED11 = LED - 5mm [color="Red (633nm)" package="5 mm [THT]"]
  bc547 = NPN-Transistor [package="TO92 [THT]"]
  LED9 = LED - 5mm [color="Red (633nm)" package="5 mm [THT]"]

nets:
  N1: Part1.VCC, VCC1.+, 74HC1.connector15, bc547.C
  N2: Part1.GND, VCC1.-, LED1.cathode, 74HC1.connector7, LED2.cathode, LED7.cathode, LED8.cathode, LED10.cathode, LED11.cathode, LED9.cathode
  N3: Part1.AUD, 74HC1.connector13, bc547.B
  N4: R1.Pin_0, bc547.E
  N5: R1.Pin_1, LED1.anode
  N6: 74HC1.connector0, LED8.anode
  N7: 74HC1.connector1, LED4.anode
  N8: 74HC1.connector2, LED3.anode
  N9: 74HC1.connector3, LED5.anode
  N10: 74HC1.connector4, LED9.anode
  N11: 74HC1.connector5, LED10.anode
  N12: 74HC1.connector6, LED6.anode
  N13: 74HC1.connector8, LED11.anode
  N14: 74HC1.connector9, LED7.anode
  N15: 74HC1.connector10, LED2.anode
  N16: 74HC1.connector12, 74HC1.connector14
