# Fritzing sketch id756_audio_led_chaser_0 (saved by Fritzing 0.9.3b)
circuit board: 6.16757cm x 3.07487cm
breadboards: 1

parts:
  Part1 = Breakout Board for Electret Microphone
  Q1 = NPN-Transistor [part_number=BC547 package="TO92 [THT]"]
  VCC1 = Battery block 9V
  LED2 = LED - 3mm [color="Red (633nm)" package="3 mm [THT]"]
  LED1 = LED - 3mm [color="Red (633nm)" package="3 mm [THT]"]
  LED3 = LED - 3mm [color="Red (633nm)" package="3 mm [THT]"]
  LED4 = LED - 3mm [color="Red (633nm)" package="3 mm [THT]"]
  LED5 = LED - 3mm [color="Red (633nm)" package="3 mm [THT]"]
  LED6 = LED - 3mm [color="Red (633nm)" package="3 mm [THT]"]
  LED7 = LED - 3mm [color="Red (633nm)" package="3 mm [THT]"]
  LED8 = LED - 3mm [color="Red (633nm)" package="3 mm [THT]"]
  LED9 = LED - 3mm [color="Red (633nm)" package="3 mm [THT]"]
  LED10 = LED - 3mm [color="Red (633nm)" package="3 mm [THT]"]
  LED11 = LED - 3mm [color="Red (633nm)" package="3 mm [THT]"]
  R1 = Resistor [tolerance=±5% resistance=1k package="2512 [SMD]"]
  74HC1 = IC Johnson Decade 74HC4017 [chip_label=74HC4017]

nets:
  N1: Part1.VCC, Q1.C, VCC1.+, 74HC1.connector15
  N2: Part1.GND, VCC1.-, LED2.cathode, LED1.anode, LED3.cathode, LED4.cathode, LED5.cathode, LED6.cathode, LED7.cathode, LED8.cathode, LED9.cathode, LED10.cathode, LED11.cathode, 74HC1.connector7
  N3: Part1.AUD, Q1.B, 74HC1.connector13
  N4: Q1.E, R1.Pin_0
  N5: LED2.anode, 74HC1.connector2
  N6: LED1.cathode, R1.Pin_1
  N7: LED3.anode, 74HC1.connector1
  N8: LED4.anode, 74HC1.connector3
  N9: LED5.anode, 74HC1.connector6
  N10: LED6.anode, 74HC1.connector9
  N11: LED7.anode, 74HC1.connector0
  N12: LED8.anode, 74HC1.connector4
  N13: LED9.anode, 74HC1.connector5
  N14: LED10.anode, 74HC1.connector8
  N15: LED11.anode, 74HC1.connector10
  N16: 74HC1.connector12, 74HC1.connector14
