# Fritzing sketch id759_proj21_0 (saved by Fritzing 0.9.2b)
breadboards: 1

parts:
  Componente1 = Arduino Uno (Rev3)
  U1 = MAX7219 [package=dil24]
  R1 = Resistor [tolerance=±5% resistance=1k package=THT]
  Disp1 = LBT2088AH [part_number=LBT2088AH]

nets:
  N1: Componente1.D2, U1.DIN
  N2: Componente1.D3_PWM, U1.LOAD
  N3: Componente1.D4, U1.CLK
  3V3: Componente1.3V3, U1.VCC, R1.Pin_1
  GND: Componente1.GND, U1.GND, U1.GND2
  N4: U1.DIG0, Disp1.pin_13
  N5: U1.DIG4, Disp1.pin_6
  N6: U1.DIG6, Disp1.pin_15
  N7: U1.DIG2, Disp1.pin_4
  N8: U1.DIG3, Disp1.pin_10
  N9: U1.DIG7, Disp1.pin_16
  N10: U1.DIG5, Disp1.pin_11
  N11: U1.DIG1, Disp1.pin_3
  N12: U1.SEGA, Disp1.pin2
  N13: U1.SEGF, Disp1.pin_14
  N14: U1.SEGB, Disp1.pin_7
  N15: U1.SEGG, Disp1.pin_9
  N16: U1.ISET, R1.Pin_0
  N17: U1.SEGC, Disp1.pin1
  N18: U1.SEGE, Disp1.pin_8
  N19: U1.SEGDP, Disp1.pin_5
  N20: U1.SEGD, Disp1.pin_12
