# Fritzing sketch id760_Aurdino_RAdar_0 (saved by Fritzing 0.9.3b)
breadboards: 1

parts:
  Part1 = Arduino Uno (Rev3)
  hc-sr1 = hc-sr04
  M1 = Dagu DGServo 9g (Pan and tilt) [part_number=RS001B]
  J1 = Piezo Speaker

nets:
  N1: Part1.D9_PWM, M1.pulse
  GND: Part1.GND, hc-sr1.GND, M1.gnd, J1.pin1
  N2: Part1.D2, hc-sr1.Echo
  N3: Part1.D3_PWM, hc-sr1.Trig
  N4: Part1.D4, J1.pin2
  VCC: Part1.5V, hc-sr1.VCC, M1.vcc

notes:
  Trigger On D3
  Echo On D2
  servo pin D9
  Buzzer Toggle D4
