# Fritzing sketch id762_reading_light_0 (saved by Fritzing 0.9.2b)
breadboards: 1

parts:
  Part1 = Arduino Nano (Rev3.0)
  RE1 = Rotary Encoder [package=THT]
  Part2 = adafruit [part_number=1463]
  PIR1 = PIR_sensor
  R1 = Resistor [tolerance=±5% resistance=10k package="0603 [SMD]"]

nets:
  N1: Part1.GND, RE1.EncoderPinB, Part2.connector21, PIR1.connector3, R1.Pin_1
  N2: Part1.D3, R1.Pin_0
  N3: Part1.D6, Part2.connector18
  N4: Part1.D9, PIR1.connector2
  N5: Part1.5V, RE1.EncoderPinA, Part2.connector20, PIR1.connector1
