# Fritzing sketch id763_AutoClock_0 (saved by Fritzing 0.9.3b)
breadboards: 1

parts:
  WeMos_D1_Mini1 = WeMos D1 Mini
  WeMos_D1_Mini_OLED_Shield1 = WeMos D1 Mini OLED Shield

nets:
  3V3: WeMos_D1_Mini1.3V3, WeMos_D1_Mini_OLED_Shield1.3V3
  N1: WeMos_D1_Mini1.D1, WeMos_D1_Mini_OLED_Shield1.D1
  N2: WeMos_D1_Mini1.D2, WeMos_D1_Mini_OLED_Shield1.D2
  N3: WeMos_D1_Mini1.D3, WeMos_D1_Mini_OLED_Shield1.RST
  N4: WeMos_D1_Mini1.G, WeMos_D1_Mini_OLED_Shield1.G
