# Fritzing sketch id764_Untitled_Sketch_0 (saved by Fritzing 0.9.3b)
breadboards: 1

parts:
  Part1 = adafruit
  R1 = PHOTOCELL [package=photocell-kit]
  Q1 = PNP-Transistor [package="TO92 [THT]"]
  Q2 = PNP-Transistor [package="TO92 [THT]"]
  LED1 = smd LED [color="Red (633nm)" package="0805 [SMD]"]
  LED2 = smd LED [color="Red (633nm)" package="1206 [SMD]"]
  R2 = Resistor [tolerance=±5% resistance=220 package="1206 [SMD]"]
  R3 = Resistor [tolerance=±5% resistance=220 package="1206 [SMD]"]
  R4 = Resistor [tolerance=±5% resistance=220 package="0402 [SMD]"]
  VCC1 = Battery

nets:
  N1: Part1.connector28, Part1.connector30, Q1.E, Q2.E, VCC1.+
  N2: Part1.connector29, R1.P$2, R2.Pin_1, R3.Pin_1, R4.Pin_1, VCC1.-
  N3: Part1.connector31, Q1.B
  N4: Part1.connector32, R1.P$1, R4.Pin_0
  N5: Part1.connector35, Q2.B
  N6: Q1.C, LED1.cathode
  N7: Q2.C, LED2.cathode
  N8: LED1.anode, R3.Pin_0
  N9: LED2.anode, R2.Pin_0
