# Fritzing sketch id765_Untitled_Sketch_WYuNyi4_0 (saved by Fritzing 0.9.3b)
circuit board: 8.46667cm x 5.64444cm
breadboards: 1

parts:
  R1 = PHOTOCELL [package=photocell-kit]
  LED1 = smd LED [color="Red (633nm)" package="0805 [SMD]"]
  R2 = Resistor [tolerance=±5% resistance=220 package="1206 [SMD]"]
  R3 = Resistor [tolerance=±5% resistance=220 package="1206 [SMD]"]
  VCC1 = Battery
  Q2 = PNP-Transistor [package="TO92 [THT]"]
  R5 = Resistor [tolerance=±5% resistance=220 package=THT]
  R8 = Resistor [tolerance=±5% resistance=220 package=THT]
  Part1 = adafruit
  Q1 = PNP-Transistor [package="TO92 [THT]"]
  LED2 = smd LED [color="Red (633nm)" package="1206 [SMD]"]
  R9 = Trimmer Potentiometer [maximum_resistance=10kΩ package=THT]

nets (from the schematic view):
  N1: R1.P$1, R1.P$2, R2.Pin_1, R3.Pin_1, VCC1.-, Part1.connector29, Part1.connector32, R9.leg1, R9.wiper, R9.leg2
  N2: LED1.cathode, R3.Pin_0
  N3: LED1.anode, Q1.C
  N4: R2.Pin_0, LED2.cathode
  N5: VCC1.+, Q2.E, Part1.connector28, Part1.connector30, Q1.E
  N6: Q2.B, R5.Pin_1
  N7: Q2.C, LED2.anode
  N8: R5.Pin_0, Part1.connector35
  N9: R8.Pin_0, Part1.connector31
  N10: R8.Pin_1, Q1.B
