# Fritzing sketch id766_Untitled_Sketch_0 (saved by Fritzing 0.9.3b)
breadboards: 1

parts:
  Componente1 = Arduino Uno (Rev3)
  SW1 = DIP Switch 8 Position [package=dipswitch-08]
  M1 = DC Motor
  OMRON1 = OMRON PCB Power Relay – G5LE [part_number="G5LE-1\n" package=THT]

nets:
  N1: Componente1.D8, SW1.2
  N2: Componente1.D9_PWM, SW1.3
  N3: Componente1.D10_PWM/SS, OMRON1.C
  N4: Componente1.GND, SW1.14, SW1.15, SW1.16, M1.pin_1, OMRON1.COIL2
  N5: Componente1.D7, SW1.1
  N6: Componente1.5V, OMRON1.COIL1
  N7: M1.pin_2, OMRON1.B
