# Fritzing sketch id768_Dice_Roll_0 (saved by Fritzing 0.9.3b)
breadboards: 1

parts:
  Part1 = Arduino Uno (Rev3)
  LED1 = LED - 5mm [color="Red (633nm)" package="5 mm [THT]"]
  LED2 = LED - 5mm [color="Red (633nm)" package="5 mm [THT]"]
  LED3 = LED - 5mm [color="Red (633nm)" package="5 mm [THT]"]
  LED4 = LED - 5mm [color="Red (633nm)" package="5 mm [THT]"]
  LED5 = LED - 5mm [color="Red (633nm)" package="5 mm [THT]"]
  LED6 = LED - 5mm [color="Red (633nm)" package="5 mm [THT]"]
  LED7 = LED - 5mm [color="Red (633nm)" package="5 mm [THT]"]
  R1 = Resistor [tolerance=±5% resistance=220 package=THT]
  R2 = Resistor [tolerance=±5% resistance=220 package=THT]
  R3 = Resistor [tolerance=±5% resistance=220 package=THT]
  R4 = Resistor [tolerance=±5% resistance=220 package=THT]
  R5 = Resistor [tolerance=±5% resistance=220 package=THT]
  R6 = Resistor [tolerance=±5% resistance=220 package=THT]
  R7 = Resistor [tolerance=±5% resistance=220 package=THT]
  S1 = Pushbutton [package="[THT]"]
  R8 = Resistor [tolerance=±5% resistance=220 package=THT]

nets:
  N1: Part1.D8, LED7.cathode
  N2: Part1.D9_PWM, Part1.5V, S1.Pin_3, S1.Pin_4
  N3: Part1.D2, LED1.cathode
  N4: Part1.D3_PWM, LED4.cathode
  N5: Part1.D4, LED6.cathode
  N6: Part1.D5_PWM, LED2.cathode
  N7: Part1.D6_PWM, LED3.cathode
  N8: Part1.D7, LED5.cathode
  N9: Part1.GND, R1.Pin_1, R2.Pin_1, R3.Pin_0, R4.Pin_1, R5.Pin_1, R6.Pin_1, R7.Pin_1, R8.Pin_0
  N10: LED1.anode, R2.Pin_0
  N11: LED2.anode, R1.Pin_0
  N12: LED3.anode, R3.Pin_1
  N13: LED4.anode, R4.Pin_0
  N14: LED5.anode, R7.Pin_0
  N15: LED6.anode, R6.Pin_0
  N16: LED7.anode, R5.Pin_0
  N17: S1.Pin_1, S1.Pin_2, R8.Pin_1
