# Fritzing sketch id769_Artifical_Pancreas_System_No.1_0 (saved by Fritzing 0.9.3b)
breadboards: 1

parts:
  R1 = Resistor [tolerance=±5% resistance=220 package=THT]
  R2 = Resistor [tolerance=±5% resistance=220 package=THT]
  Q1 = Basic FET N-Channel [package="TO220 [THT]"]
  R3 = TRIMPOT [package=3386u]
  R4 = TRIMPOT [package=3386u]
  R5 = TRIMPOT [package=3386u]
  VCC1 = 4 x AAA Battery Mount
  M1 = DC Motor

nets:
  N1: R1.Pin_0, Q1.gate, VCC1.+, M1.pin_2
  N2: R1.Pin_1, R2.Pin_1
  N3: R2.Pin_0, R5.CW, VCC1.-, M1.pin_1
  N4: Q1.source, R3.WIPER
  N5: R3.CW, R4.WIPER
  N6: R4.CW, R5.WIPER

notes:
  Conductivity Sensor
