# Fritzing sketch id770_progettopark_finale_0 (saved by Fritzing 0.9.0b)
breadboards: 1

parts:
  Intel_Galileo = Intel Galileo
  S1 = Momentary Switch [package=ksa_sealed_tac_switch]
  Display_7_Segmenti = 7 Segment Display
  R3 = Resistor [package="2010 [SMD]"]
  R4 = Resistor [package="2010 [SMD]"]
  R5 = Resistor [package="2010 [SMD]"]
  R6 = Resistor [package="2010 [SMD]"]
  R7 = Resistor [package="2010 [SMD]"]
  R8 = Resistor [package="2010 [SMD]"]
  R9 = Resistor [package="2010 [SMD]"]
  Tower_Pro_SG90_9G = Basic Servo
  R10 = Resistor [package="2512 [SMD]"]
  S2 = Pushbutton [package="[SMD]"]
  R11 = Resistor [package="2512 [SMD]"]

nets:
  N1: Intel_Galileo.D10_PWM/SS, Tower_Pro_SG90_9G.pulse
  N2: Intel_Galileo.D11_PWM/MOSI, Intel_Galileo.5V
  N3: Intel_Galileo.D12/MISO, R11.Pin_0
  N4: Intel_Galileo.D0/RX, R3.Pin_0
  N5: Intel_Galileo.D1/TX, R4.Pin_0
  N6: Intel_Galileo.D2, R5.Pin_0
  N7: Intel_Galileo.D3_PWM, R6.Pin_0
  N8: Intel_Galileo.D4, R7.Pin_0
  N9: Intel_Galileo.D5_PWM, R8.Pin_0
  N10: Intel_Galileo.D6_PWM, R9.Pin_0
  GND: Intel_Galileo.GND, Tower_Pro_SG90_9G.gnd
  N11: S1.1, S1.3, Display_7_Segmenti.common_cathode, S2.Pin_1, S2.Pin_2, S2.Pin_3, S2.Pin_4
  N12: S1.2, S1.4
  N13: Display_7_Segmenti.Segment_A#1, R3.Pin_1
  N14: Display_7_Segmenti.Segment_F, R8.Pin_1
  N15: Display_7_Segmenti.Segment_E, R7.Pin_1
  N16: Display_7_Segmenti.Segment_D, R6.Pin_1
  N17: Display_7_Segmenti.Segment_C, R5.Pin_1
  N18: Display_7_Segmenti.Segment_B, R4.Pin_1
  N19: Display_7_Segmenti.Segment_A#10, R9.Pin_1
  N20: Tower_Pro_SG90_9G.vcc, R10.Pin_1, R11.Pin_1

notes:
  Prototipo per la creazione di una sbarra automatica per il parcheggio di veicoli in grado di tener conto dei posti disponibili.
  Prototype for the creation of an automatic vehicles parking barrier with real-time counter of available parking lots
