# Fritzing sketch id772_Automatic_plant_watering_v_1_1_0 (saved by Fritzing 0.9.3b)

parts:
  Часть1 = Troyka Potentiometer
  Часть2 = Troyka Led
  Часть4 = Real Time Clock Module - DS1307 RTC Breakout Board
  U1 = RELAY [package=relay-jzc]
  Часть5 = Soil Moisture Sensor
  S1 = SWITCH-MOMENTARY-2 [package=reed_switch_pth]
  Часть8 = Troyka Shield
  Q1 = MOSFET-NCHANNEL [package=sot23-3]
  M1 = prefix0000

nets:
  N1: Часть1.connector8, Часть8.connector79
  N2: Часть1.connector9, Часть8.connector85
  N3: Часть1.connector10, Часть8.connector91
  N4: Часть2.connector8, Часть8.connector46
  N5: Часть2.connector9, Часть8.connector60
  N6: Часть2.connector10, Часть8.connector74
  N7: Часть4.5V, Часть8.connector19
  N8: Часть4.GND, Часть8.connector31
  N9: Часть4.SCL, Часть8.connector24
  N10: Часть4.SDA, Часть8.connector25
  N11: U1.COIL2, Часть8.connector73
  N12: U1.NO, M1.connector0
  N13: U1.COIL1, Часть8.connector15
  N14: Часть5.SIG, Часть8.connector29
  N15: Часть5.VCC, Q1.D
  N16: S1.1, Часть8.connector49, Часть8.connector50
  N17: S1.2, Часть8.connector63
  N18: Часть8.connector20, Q1.G

notes:
  9V
  ISP Quad 7-segment Display
  7 сегментный дисплей
  WaterPump
  Помпа
  MOSFET Key
  Мосфет ключ
  Sensor
  Сенсор
  RTC
  Часы
  Potentiometer Потенциометр
  Raley
  Реле
  LED
  Светодиод
  Reed switch
  Геркон
