# Fritzing sketch id773_shutter_0 (saved by Fritzing 0.9.2b)
breadboards: 1

parts:
  LCD1 = LCD screen
  Part1 = Arduino Uno (Rev3)
  R1 = Resistor [tolerance=±5% resistance=220 package="2512 [SMD]"]
  R2 = Rotary Potentiometer (Large) [maximum_resistance=100kΩ package=THT]
  Part2 = Real Time Clock Module - DS1307 RTC Breakout Board

nets:
  GND: LCD1.VSS, LCD1.R/W, Part1.GND, R1.Pin_1, R2.leg1, Part2.GND
  5V: LCD1.VDD, LCD1.LED+, Part1.5V, R2.leg2, Part2.5V
  N1: LCD1.V0, R2.wiper
  N2: LCD1.RS, Part1.D12/MISO
  N3: LCD1.E, Part1.D11_PWM/MOSI
  N4: LCD1.DB4, Part1.D5_PWM
  N5: LCD1.DB5, Part1.D9_PWM
  N6: LCD1.DB6, Part1.D3_PWM
  N7: LCD1.DB7, Part1.D2
  N8: LCD1.LED-, R1.Pin_0
  N9: Part1.A4/SDA, Part2.SDA
  N10: Part1.A5/SCL, Part2.SCL
