# Fritzing sketch id775_Automatic_Traffic_Lights_fgLaNZl_0 (saved by Fritzing 0.9.3b)
breadboards: 1

parts:
  Part1 = Arduino Mega 2560 (Rev3)
  DI1 = 7-Segment LED Display [package=THT]
  DI2 = 7-Segment LED Display [package=THT]
  LED1 = LED - 5mm [color="Red (660nm)" package="5 mm [THT]"]
  LED2 = LED - 5mm [color="Yellow (595nm)" package="5 mm [THT]"]
  LED3 = LED - 5mm [color="Green (570nm)" package="5 mm [THT]"]
  R1 = Resistor [tolerance=±1% resistance=220 package=THT]
  R2 = Resistor [tolerance=±1% resistance=220 package=THT]
  R3 = Resistor [tolerance=±1% resistance=220 package=THT]

nets:
  N1: Part1.GND, LED1.cathode, LED2.cathode, LED3.cathode
  N2: Part1.D12_PWM, R1.Pin_1
  N3: Part1.D11_PWM, R2.Pin_1
  N4: Part1.D10_PWM, R3.Pin_1
  N5: Part1.5V, DI1.commAnode#2, DI2.commAnode#2
  N6: Part1.D40, DI1.cathodeA
  N7: Part1.D41, DI2.cathodeB
  N8: Part1.D42, DI1.cathodeB
  N9: Part1.D43, DI2.cathodeA
  N10: Part1.D44, DI1.cathodeC
  N11: Part1.D45, DI2.cathodeC
  N12: Part1.D46, DI1.cathodeD
  N13: Part1.D47, DI2.cathodeD
  N14: Part1.D48, DI1.cathodeE
  N15: Part1.D49, DI2.cathodeE
  N16: Part1.D50, DI1.cathodeF
  N17: Part1.D51, DI2.cathodeF
  N18: Part1.D52, DI1.cathodeG
  N19: Part1.D53, DI2.cathodeG
  N20: LED1.anode, R3.Pin_0
  N21: LED2.anode, R2.Pin_0
  N22: LED3.anode, R1.Pin_0
