# Fritzing sketch id777_Automoviva_SensorCinto_0 (saved by Fritzing 0.9.3b)
breadboards: 1

parts:
  Componente1 = Arduino Uno (Rev3)
  J1 = Piezo Speaker
  hc-sr1 = hc-sr04

nets:
  N1: Componente1.D9_PWM, J1.pin2
  N2: Componente1.D4, hc-sr1.Trig
  N3: Componente1.D5_PWM, hc-sr1.Echo
  N4: J1.pin1, hc-sr1.GND
