# Fritzing sketch id778_Autopilot_0 (saved by Fritzing 0.9.2b)
breadboards: 1

parts:
  J1 = Screw terminal - 2 pins [package=THT]
  Raspberry_Pi2 = Raspberry Pi B rev2
  IC1 = IC, DIP package, 8 pins [chip_label=IC]
  IC2 = IC, DIP package, 8 pins [chip_label=IC]
  IC3 = IC, DIP package, 8 pins [chip_label=IC]
  IC4 = IC, DIP package, 8 pins [chip_label=IC]
  J2 = Screw terminal - 2 pins [package=THT]
  J3 = Screw terminal - 2 pins [package=THT]
  J4 = Screw terminal - 2 pins [package=THT]
  J5 = Screw terminal - 2 pins [package=THT]
  J6 = Screw terminal - 2 pins [package=THT]

nets:
  N1: J1.pin1, IC4.pin7
  N2: J1.pin2, IC1.pin6
  N3: Raspberry_Pi2.5V, IC1.pin8, IC2.pin8, IC3.pin8, IC4.pin8
  N4: Raspberry_Pi2.GND, IC1.pin4, IC2.pin4, IC3.pin4, IC4.pin4
  N5: Raspberry_Pi2.GPIO_27, IC3.pin1
  N6: Raspberry_Pi2.GPIO_22, IC4.pin1
  N7: Raspberry_Pi2.GPIO_10, IC1.pin3, IC2.pin3, IC3.pin3, IC4.pin3
  N8: Raspberry_Pi2.GPIO_11, IC1.pin2, IC2.pin2, IC3.pin2, IC4.pin2
  N9: Raspberry_Pi2.GPIO_8, IC1.pin1
  N10: Raspberry_Pi2.GPIO_7, IC2.pin1
  N11: IC1.pin5, J2.pin1
  N12: IC1.pin7, J4.pin2
  N13: IC2.pin5, J3.pin2
  N14: IC2.pin6, J3.pin1
  N15: IC2.pin7, J6.pin1
  N16: IC3.pin5, J4.pin1
  N17: IC3.pin6, J6.pin2
  N18: IC3.pin7, J2.pin2
  N19: IC4.pin5, J5.pin2
  N20: IC4.pin6, J5.pin1

notes:
  SCK
  MOSI
  CS
