# Fritzing sketch id779_AutoPult_0 (saved by Fritzing 0.8.7b)
breadboards: 1

parts:
  U1 = L298 [package=multiwatt15]
  C1 = Ceramic Capacitor [capacitance=100nF package="100 mil [THT, multilayer]"]
  IC1 = PICAXE-08M [package=THT]

nets:
  N1: U1.CSA, IC1.Serial_Out_/_Out_0_/_Infraout
  N2: U1.OUT1, IC1.In/Out_2_/_ADC_2_/_PWM_2
  N3: U1.VS, IC1.In/Out_1_/_ADC_1
  N4: U1.IN1, IC1.In_3_/_Infrain
  N5: U1.GND, IC1.+V
  N6: U1.IN4, IC1.Serial_In
  N7: U1.OUT4, IC1.0V
  N8: U1.CSB, C1.0
  N9: C1.1, IC1.In/Out_4_/_ADC_4
