# Fritzing sketch id780_AVA_0 (saved by Fritzing 0.9.3b)
breadboards: 1

parts:
  Wireless_Transmitter_(MKR_1000) = Arduino-MKR1000
  Accelerometer_(ADXL_337) = Triple Axis Accelerometer Breakout - ADXL335
  Battery = Battery Holders [package=lipo-1100mAh]
  Switch = SWITCH-MOMENTARY-2 [package=tactile_switch_tall]

nets:
  N1: Wireless_Transmitter_(MKR_1000).connector1, Accelerometer_(ADXL_337).XOUT
  N2: Wireless_Transmitter_(MKR_1000).connector2, Accelerometer_(ADXL_337).YOUT
  N3: Wireless_Transmitter_(MKR_1000).connector3, Accelerometer_(ADXL_337).ZOUT
  N4: Wireless_Transmitter_(MKR_1000).connector17, Wireless_Transmitter_(MKR_1000).connector23
  N5: Wireless_Transmitter_(MKR_1000).connector19, Accelerometer_(ADXL_337).ST
  N6: Wireless_Transmitter_(MKR_1000).connector24, Accelerometer_(ADXL_337).GND
  N7: Wireless_Transmitter_(MKR_1000).connector25, Accelerometer_(ADXL_337).VCC
  N8: Battery.+, Switch.1
