# Fritzing sketch id781_avatar_0 (saved by Fritzing 0.9.3b)
circuit board: 6.88566cm x 5.36311cm

parts:
  LED = LED - 5mm [color="Red (633nm)" package="5 mm [THT]"]
  BlueTooth = Bluetooth HC-05 Macho
  Prox = TMP36 Temperature Sensor [package="TO92 [THT]"]
  Prog/BT = female pin header, 2 pins [form="♀ (female)"]
  LCD_16x2_i2c = female pin header, 4 pins [form="♀ (female)"]
  HC-SR04 = hc-sr04
  Buzz = Piezo Speaker
  HX_711 = female pin header, 4 pins [form="♀ (female)"]
  Rotary = female pin header, 5 pins [form="♀ (female)"]
  Arduino1 = Arduino Uno (Rev3)

nets:
  GND: LED.cathode, BlueTooth.GND, LCD_16x2_i2c.pin1, HC-SR04.GND, Buzz.pin2, HX_711.pin4, Rotary.pin1, Arduino1.GND
  N1: LED.anode, Arduino1.D13/SCK
  N2: BlueTooth.TXD, Arduino1.D0/RX
  N3: BlueTooth.RXD, Arduino1.D1/TX
  N4: BlueTooth.VCC, Prog/BT.pin1
  N5: Prox.+Vs, Arduino1.D2
  N6: Prox.Vout, Arduino1.D3_PWM
  N7: Prox.GND, Arduino1.D4
  VCC: Prog/BT.pin2, LCD_16x2_i2c.pin2, HC-SR04.VCC, HX_711.pin1, Rotary.pin2, Arduino1.5V
  N8: LCD_16x2_i2c.pin3, Arduino1.A4/SDA
  N9: LCD_16x2_i2c.pin4, Arduino1.A5/SCL
  N10: HC-SR04.Trig, Arduino1.D8
  N11: HC-SR04.Echo, Arduino1.D7
  N12: Buzz.pin1, Arduino1.D9_PWM
  N13: HX_711.pin2, Arduino1.D6_PWM
  N14: HX_711.pin3, Arduino1.D5_PWM
  N15: Rotary.pin3, Arduino1.D12/MISO
  N16: Rotary.pin4, Arduino1.D11_PWM/MOSI
  N17: Rotary.pin5, Arduino1.D10_PWM/SS

notes:
  AVATAR-@LaurentAldon
