# Fritzing sketch id782_Untitled_Sketch_0 (saved by Fritzing 0.9.3b)
breadboards: 1

parts:
  Part1 = Arduino Uno (Rev3)
  Part2 = Soil Moisture Sensor
  T1 = LM35 Temperature Sensor [package="TO92 [THT]"]
  R2 = Resistor [tolerance=±5% resistance=220 package=THT]
  Part3 = XBee Explorer Regulated
  Part4 = Arduino Uno (Rev3)
  Part5 = XBee Explorer Regulated
  U2 = XBEE-1 [package=xbee-1_lock]  # not connected
  U3 = XBEE-1 [package=xbee-1_lock]  # not connected
  R3 = Photocell (LDR) [package=THT]
  pH_Circuit1 = pH Circuit

nets:
  N1: Part1.A0, R2.Pin_0, R3.pin_1
  N2: Part1.A1, T1.Vout
  N3: Part1.A2, Part2.SIG
  N4: Part1.A3, pH_Circuit1.PRB
  GND: Part1.GND, Part2.GND, T1.GND, Part3.GND, R3.pin_0, pH_Circuit1.GND
  N5: Part1.D0/RX, Part3.DOUT
  N6: Part1.D1/TX, Part3.DIN
  VCC: Part2.VCC, pH_Circuit1.Vcc
  N7: T1.+Vs, R2.Pin_1
  GND_2: Part4.GND, Part5.GND
  N8: Part4.D0/RX, Part5.DOUT
  N9: Part4.D1/TX, Part5.DIN
  5V: Part4.5V, Part5.5V

notes:
  1-TEMP SENSOR
  2-MOISTUR SESNOR
  3-LDR
