# Fritzing sketch id783_servo_ultrasonic_0 (saved by Fritzing 0.9.3b)
breadboards: 1

parts:
  L298N_Module = Ponte-H L298N
  Arduino_Nano_3_0 = Arduino Nano (Rev3.0)
  VCC1 = Battery
  Power_Switch = Toggle Switch [package=THT]
  Right_Motor = DC Motor
  Left_Motor = DC Motor
  Part1 = SRF05 Ultrasonic Rangefinder
  J1 = Basic Servo

nets (from the breadboard view):
  N1: L298N_Module.connector1, Power_Switch.L2
  GND: L298N_Module.connector2, Arduino_Nano_3_0.GND, VCC1.-, Part1.connector11, J1.gnd
  5V: L298N_Module.connector3, L298N_Module.connector4, L298N_Module.connector9, L298N_Module.connector15, L298N_Module.connector16, Arduino_Nano_3_0.5V, Part1.connector8, J1.vcc
  N2: L298N_Module.connector5, Arduino_Nano_3_0.D3
  N3: L298N_Module.connector6, Arduino_Nano_3_0.D5
  N4: L298N_Module.connector7, Arduino_Nano_3_0.D6
  N5: L298N_Module.connector8, Arduino_Nano_3_0.D9
  N6: L298N_Module.connector10, Left_Motor.pin_2
  N7: L298N_Module.connector11, Left_Motor.pin_1
  N8: L298N_Module.connector13, Right_Motor.pin_2
  N9: L298N_Module.connector14, Right_Motor.pin_1
  N10: Arduino_Nano_3_0.D10, J1.pulse
  N11: Arduino_Nano_3_0.D12/MISO, Part1.connector9
  N12: Arduino_Nano_3_0.D13/SCK, Part1.connector10
  N13: VCC1.+, Power_Switch.COM

notes:
  18650 Batteries
  Vcc = 7.4 volts
  Ultrasonic
  HC-SR04
  L298N Module
  S3003 Standard Servo
  Arduino Nano R3
