# Fritzing sketch id784_Assignment_3 (saved by Fritzing 0.9.3b)
circuit board: 8.46667cm x 5.64444cm
breadboards: 1

parts:
  Part1 = Arduino Uno (Rev3)
  T1 = LM35 Temperature Sensor [package="TO92 [THT]"]
  hc-sr1 = hc-sr04
  S1 = Momentary Switch [package=ksa_sealed_tac_switch]
  R1 = Resistor [tolerance=±5% resistance=10k package="2010 [SMD]"]
  LCD1 = LCD screen
  R2 = Resistor [tolerance=±5% resistance=1k package="2010 [SMD]"]
  R3 = Resistor [tolerance=±5% resistance=10k package="2010 [SMD]"]
  R4 = Resistor [tolerance=±5% resistance=220 package="2010 [SMD]"]

nets:
  N1: Part1.A1, T1.Vout
  N2: Part1.D9_PWM, hc-sr1.Trig
  N3: Part1.D10_PWM/SS, hc-sr1.Echo
  N4: Part1.D11_PWM/MOSI, LCD1.E
  N5: Part1.D12/MISO, LCD1.RS
  N6: Part1.D13/SCK, S1.2, R1.Pin_0
  N7: Part1.D2, LCD1.DB7
  N8: Part1.D3_PWM, LCD1.DB6
  N9: Part1.D4, LCD1.DB5
  N10: Part1.D5_PWM, LCD1.DB4
  5V: Part1.5V, T1.+Vs, hc-sr1.VCC, S1.4, LCD1.VDD, R3.Pin_1, R4.Pin_0
  GND: Part1.GND, T1.GND, hc-sr1.GND, R1.Pin_1, LCD1.VSS, LCD1.R/W, LCD1.LED-, R2.Pin_0
  N11: LCD1.V0, R2.Pin_1, R3.Pin_0
  N12: LCD1.LED+, R4.Pin_1
