# Fritzing sketch id784_bootloader_0 (saved by Fritzing 0.9.0b)
circuit board: 9.906cm x 5.14773cm
breadboards: 1

parts:
  CON1 = USB connector [package=THT]
  R7 = Resistor [tolerance=±5% resistance=1.5k package=THT]
  LED1 = LED - 5mm [color="Green (555nm)" package="5 mm [THT]"]
  LED2 = LED - 5mm [color="Red (633nm)" package="5 mm [THT]"]
  C1 = Electrolytic Capacitor [capacitance=1µF package="100 mil [THT, electrolytic]"]
  J3 = male pin header, 2 pins [form="♂ (male)"]
  R4 = Resistor [tolerance=±5% resistance=330 package=THT]
  R4_2 = Resistor [tolerance=±5% resistance=330 package=THT]
  R2 = Resistor [tolerance=±5% resistance=68 package=THT]
  R6 = Resistor [tolerance=±5% resistance=68 package=THT]
  C1_2 = Ceramic Capacitor [capacitance=10pF package="100 mil [THT, multilayer]"]
  C2 = Ceramic Capacitor [capacitance=10pF package="100 mil [THT, multilayer]"]
  XTAL1 = Crystal [frequency="16 Mhz" package=THT]
  R3 = Resistor [tolerance=±5% resistance=220 package=THT]
  R1 = Resistor [tolerance=±5% resistance=10k package=THT]
  J2 = female pin header, 2 pins [form="♀ (female)"]
  J1 = female pin header, 2 pins [form="♀ (female)"]
  C4 = Ceramic Capacitor [capacitance=100nF package="100 mil [THT, multilayer]"]
  CON2 = shrouded pin header, 10 pins [form="♂ (shrouded male)"]
  U1 = atmega168 [package=dip]

nets:
  5V: CON1.5V, R7.Pin_1, LED1.anode, LED2.anode, C1.+, R1.Pin_1, J1.pin1, C4.1, U1.VCC, U1.AVCC, U1.AREF
  N1: CON1.d-, R7.Pin_0, R6.Pin_0
  N2: CON1.d+, R2.Pin_0
  N3: CON1.GND, CON1.chassis5, CON1.chassis6, C1.-, J3.pin2, C4.0, U1.GND#21
  N4: LED1.cathode, R4.Pin_0
  N5: LED2.cathode, R4_2.Pin_1
  N6: J3.pin1, U1.A2
  N7: R4.Pin_1, U1.A1
  N8: R4_2.Pin_0, U1.A0
  N9: R2.Pin_1, U1.D2, U1.D9_(PWM)
  N10: R6.Pin_1, U1.D8
  N11: C1_2.0, XTAL1.pin_0, U1.XLAT1
  N12: C1_2.1, C2.1, CON2.pin1, CON2.pin2, U1.GND#7
  N13: C2.0, XTAL1.pin_1, U1.XLAT2
  N14: R3.Pin_0, U1.D1_(TX)
  N15: R3.Pin_1, CON2.pin4
  N16: R1.Pin_0, J2.pin1, U1.RESET
  N17: J2.pin2, CON2.pin8, U1.D10_(PWM)
  N18: J1.pin2, CON2.pin5
  N19: CON2.pin3, U1.D0_(RX)
  N20: CON2.pin6, U1.D11_(PWM)
  N21: CON2.pin9, U1.D13
  N22: CON2.pin10, U1.D12
