# Fritzing sketch id785_JTAG_AVR_Dragon_ATMega2560R3_0 (saved by Fritzing 0.9.3b)

parts:
  Bauteil1 = Arduino Mega 2560 (Rev3)
  Header1 = 10Pin Dual Row Header
  Header2 = 2pin header
  Header3 = 2pin header
  Header4 = 2pin header

nets:
  N1: Bauteil1.RESET, Header1.connector6
  N2: Header1.connector1, Header3.connector0
  N3: Header1.connector2, Header1.connector10, Header4.connector1
  N4: Header1.connector3, Header2.connector0
  N5: Header1.connector4, Header4.connector0
  N6: Header1.connector5, Header3.connector1
  N7: Header1.connector9, Header2.connector1

notes:
  doppelreihiger JTAG Anschluss auf dem AVR-Dragon
  Pin 6 Reset (optional)
  is not nessesary, only for certain scenarios
