# Fritzing sketch id788_single_digit_dice_0 (saved by Fritzing 0.9.3b)
breadboards: 2

parts:
  R1 = Resistor [tolerance=±5% resistance=10k package=THT]
  Reset = Pushbutton [package="[THT]"]
  LED1 = LED - 5mm [color="Red (633nm)" package="5 mm [THT]"]
  Atmega16 = IC, DIP package, 40 pins [chip_label="ATMEL ATMEGA 16L 8PU 1016"]
  7805 = Voltage Regulator [package=78xxl]
  VCC = 4 x AAA Battery Mount
  R2 = Resistor [tolerance=±5% resistance=220 package=THT]
  S1 = Pushbutton [package="[THT]"]
  7_Segment1 = 7 Segment Display
  R3 = Resistor [tolerance=±5% resistance=220 package=THT]
  R4 = Resistor [tolerance=±5% resistance=220 package=THT]

nets:
  N1: R1.Pin_0, Reset.Pin_1, Reset.Pin_2, LED1.anode, Atmega16.pin10, Atmega16.pin30, 7805.OUT, R3.Pin_1
  N2: R1.Pin_1, Atmega16.pin9
  N3: Reset.Pin_3, Reset.Pin_4, Atmega16.pin11, Atmega16.pin31, 7805.GND, VCC.-, R2.Pin_1, S1.Pin_1, S1.Pin_2
  N4: LED1.cathode, R2.Pin_0
  N5: Atmega16.pin21, S1.Pin_3, S1.Pin_4
  N6: Atmega16.pin34, 7_Segment1.Segment_G
  N7: Atmega16.pin35, 7_Segment1.Segment_F
  N8: Atmega16.pin36, 7_Segment1.Segment_E
  N9: Atmega16.pin37, 7_Segment1.Segment_D
  N10: Atmega16.pin38, 7_Segment1.Segment_C
  N11: Atmega16.pin39, 7_Segment1.Segment_B
  N12: Atmega16.pin40, 7_Segment1.Segment_A
  N13: 7805.IN, VCC.+
  N14: 7_Segment1.common_cathode, R3.Pin_0, R4.Pin_1

notes:
  Voltage Regulation
  Vin = 5V
  Chip: Atmega 16
