# Fritzing sketch id789_usb_avr_0 (saved by Fritzing 0.8.7b)
circuit board: 4.8cm x 3.8cm
breadboards: 1

parts:
  IC1 = MICROCONTROLLER [package=dil28-3-simon]
  RST = Pushbutton [package="[THT]"]
  USB = USB+SHIELD [package=usb-b-pth]
  D2 = Zener Diode [part_number=1N4732A breakdown_voltage=3.6V package="300 mil [THT]"]
  D1 = Zener Diode [part_number=1N4732A breakdown_voltage=3.6V package="300 mil [THT]"]
  R1 = Resistor [tolerance=±5% resistance=68 package=THT]
  R2 = Resistor [tolerance=±5% resistance=68 package=THT]
  R3 = Resistor [tolerance=±5% resistance=1M package=THT]
  J2 = female pin header, 3 pins [form="♀ (female)"]
  5V_REG = Voltage Regulator [package=to220-igo]
  C2 = Electrolytic Capacitor [capacitance=10µF package="100 mil [THT, electrolytic]"]
  C1 = Electrolytic Capacitor [capacitance=10µF package="100 mil [THT, electrolytic]"]
  IC3 = IC, DIP package, 6 pins [chip_label=DB101]
  PWRext = Screw terminal - 2 pins [package=THT]
  C3 = Ceramic Capacitor [capacitance=22pF package="100 mil [THT, multilayer]"]
  C4 = Ceramic Capacitor [capacitance=22pF package="100 mil [THT, multilayer]"]
  C5 = Ceramic Capacitor [capacitance=100nF package="100 mil [THT, multilayer]"]
  XTAL1 = Crystal [frequency="16 Mhz" package=THT]
  USB-INT = female pin header, 4 pins [form="♀ (female)"]
  R4 = Resistor [tolerance=±5% resistance=1.5k package=THT]
  BOOTLOADER_JP6 = female pin header, 2 pins [form="♀ (female)"]
  OUT2 = female pin header, 14 pins [form="♀ (female)"]
  USB-IC = female pin header, 2 pins [form="♀ (female)"]
  USB-JMP = female pin header, 2 pins [form="♀ (female)"]
  LED1 = LED - 3mm [color="Green (565nm)" part_number="LED 3MM 5V GN" package="3 mm [THT]"]
  OUT1 = female pin header, 14 pins [form="♀ (female)"]

nets:
  N1: IC1.PC6(_RESET), RST.Pin_1, RST.Pin_2, OUT1.pin1
  N2: IC1.PD0(RXD), OUT1.pin2
  N3: IC1.PD1(TXD), OUT1.pin3
  N4: IC1.PD2(INT0), USB-IC.pin2, OUT1.pin4
  N5: IC1.PD3(INT1), OUT1.pin5
  N6: IC1.PD4(XCK_T0), USB-IC.pin1, OUT1.pin6
  5V: IC1.VCC, IC1.AVCC, J2.pin2, C2.+, C5.1, USB-INT.pin1, R4.Pin_1, OUT2.pin9, LED1.anode, OUT1.pin7
  GND: IC1.GND, IC1.AGND, RST.Pin_3, RST.Pin_4, USB.P$1, USB.P$2, USB.GND, D2.anode, D1.anode, R3.Pin_0, 5V_REG.GND, C2.-, C1.-, IC3.pin6, C3.0, C4.0, C5.0, USB-INT.pin4, BOOTLOADER_JP6.pin2, OUT2.pin7, LED1.cathode, OUT1.pin8
  N7: IC1.PB6(XTAL1_TOSC1), C3.1, XTAL1.pin_0, OUT1.pin9
  N8: IC1.PB7(XTAL2_TOSC2), C4.1, XTAL1.pin_1, OUT1.pin10
  N9: IC1.PD5(T1), OUT1.pin11
  N10: IC1.PD6(AIN0), OUT1.pin12
  N11: IC1.PD7(AIN1), BOOTLOADER_JP6.pin1, OUT1.pin13
  N12: IC1.PB0(ICP), OUT1.pin14
  N13: IC1.PB1(OC1A), OUT2.pin14
  N14: IC1.PB2(SS_OC1B), OUT2.pin13
  N15: IC1.PB3(MOSI_OC2), OUT2.pin12
  N16: IC1.PB4(MISO), OUT2.pin11
  N17: IC1.PB5(SCK), OUT2.pin10
  N18: IC1.AREF, OUT2.pin8
  N19: IC1.PC0(ADC0), OUT2.pin6
  N20: IC1.PC1(ADC1), OUT2.pin5
  N21: IC1.PC2(ADC2), OUT2.pin4
  N22: IC1.PC3(ADC3), OUT2.pin3
  N23: IC1.PC4(ADC4_SDA), OUT2.pin2
  N24: IC1.PC5(ADC5_SCL), OUT2.pin1
  N25: USB.D+, D1.cathode, R2.Pin_0, R3.Pin_1
  N26: USB.D-, D2.cathode, R1.Pin_0, R4.Pin_0
  N27: USB.VBUS, J2.pin1
  N28: R1.Pin_1, USB-INT.pin2, USB-JMP.pin1
  N29: R2.Pin_1, USB-INT.pin3, USB-JMP.pin2
  N30: J2.pin3, 5V_REG.OUT
  N31: 5V_REG.IN, C1.+, IC3.pin4
  N32: IC3.pin1, PWRext.pin2
  N33: IC3.pin3, PWRext.pin1

notes:
  usb/ext
  ext:7-20VAC
  avr-usb r01 2014-02
  fritzing
