# Fritzing sketch id78_innocean_0 (saved by Fritzing 0.9.3b)
breadboards: 1

parts:
  Grove1 = Grove OLED 128x96
  부품1 = Arduino Uno (Rev3) - ICSP
  R1 = Resistor [tolerance=±5% resistance=150 package=THT]
  C1 = Electrolytic Capacitor [capacitance=1µF package="100 mil [THT, electrolytic]"]

nets:
  GND: Grove1.GND, 부품1.GND, C1.-
  VCC: Grove1.VCC, 부품1.5V, R1.Pin_0
  N1: Grove1.SDA, 부품1.A4/SDA
  N2: Grove1.SCL, 부품1.A5/SCL
  N3: R1.Pin_1, C1.+
