# Fritzing sketch id790_atmega328_0 (saved by Fritzing 0.9.3b)
breadboards: 1

parts:
  U1 = atmega328 [package=dip]
  R1 = Resistor [tolerance=±5% resistance=330 package=THT]
  LED1 = LED - 3mm [color="Red (633nm)" package="3 mm [THT]"]

nets:
  5V: U1.RESET, R1.Pin_0
  N1: U1.D13, LED1.cathode
  N2: R1.Pin_1, LED1.anode
