# Fritzing sketch id791_AWE_0 (saved by Fritzing 0.9.2b)
breadboards: 1

parts:
  Part1 = Arduino Mega 2560 (Rev3)
  VCC1 = Battery block 9V
  Part2 = EasyDriver_v44
  M1 = Stepper Motor - Bipolar

nets:
  GND: Part1.GND, VCC1.-, Part2.GND
  N1: Part1.D9_PWM, Part2.STEP
  N2: Part1.D8_PWM, Part2.DIR
  N3: VCC1.+, Part2.V+
  N4: Part2.OUT2A, M1.A
  N5: Part2.OUT2B, M1.C
  N6: Part2.OUT1A, M1.B
  N7: Part2.OUT1B, M1.D
