# Fritzing sketch id792_vyvojova_doska_pripravena_na_kontrolu_0 (saved by Fritzing 0.8.7b)
circuit board: 12cm x 12cm
breadboards: 1

parts:
  U1 = ATmega644 [package=pdpi]
  U2 = LCD-16X2 [package=lcd-16x2]
  D1 = LED_BARGRAPH_10 [package=led_bargaph_10]
  J1 = female pin header, 10 pins [form="♀ (female)"]
  J2 = female pin header, 10 pins [form="♀ (female)"]
  D5 = Rectifier Diode [part_number=1N4001 package="300 mil [THT]"]
  D6 = Rectifier Diode [part_number=1N4001 package="300 mil [THT]"]
  D7 = Rectifier Diode [part_number=1N4001 package="300 mil [THT]"]
  D8 = Rectifier Diode [part_number=1N4001 package="300 mil [THT]"]
  J5 = Screw terminal - 2 pins [package=THT]
  C2 = Electrolytic Capacitor [capacitance=4.7mF voltage=10V package="200 mil [THT, electrolytic]"]
  U3 = Voltage Regulator - 3.3V [package="TO220 [THT]"]
  U4 = Voltage Regulator - 5V [package="TO220 [THT]"]
  J6 = female pin header, 3 pins [form="♀ (female)"]
  R1 = Trimmer Potentiometer [maximum_resistance=10kΩ package=THT]
  R2 = Trimmer Potentiometer [maximum_resistance=10kΩ package=THT]
  J8 = female pin header, 20 pins [form="♀ (female)"]
  J7 = female pin header, 20 pins [form="♀ (female)"]
  J9 = female pin header, 2 pins [form="♀ (female)"]
  J10 = female pin header, 2 pins [form="♀ (female)"]
  J11 = female pin header, 2 pins [form="♀ (female)"]
  J12 = female pin header, 2 pins [form="♀ (female)"]
  J13 = female pin header, 2 pins [form="♀ (female)"]
  J14 = female pin header, 2 pins [form="♀ (female)"]
  J15 = female pin header, 16 pins [form="♀ (female)"]
  S4 = Pushbutton [package="[THT]"]
  S5 = Pushbutton [package="[THT]"]
  S6 = Pushbutton [package="[THT]"]
  R3 = Resistor [tolerance=±5% resistance=220 package=THT]
  R4 = Resistor [tolerance=±5% resistance=220 package=THT]
  R5 = Resistor [tolerance=±5% resistance=220 package=THT]
  S7 = Pushbutton [package="[THT]"]
  R6 = Resistor [tolerance=±5% resistance=220 package=THT]
  J16 = female pin header, 4 pins [form="♀ (female)"]
  J17 = female pin header, 20 pins [form="♀ (female)"]
  J18 = female pin header, 20 pins [form="♀ (female)"]
  J19 = female pin header, 20 pins [form="♀ (female)"]
  J20 = female pin header, 20 pins [form="♀ (female)"]
  S8 = Pushbutton [package="[THT]"]
  J21 = AVR ISP 6 Pin [package=2x3_lock]
  J22 = double row female pin header, 4 pins [form="♀ (female)"]
  J23 = Screw terminal - 2 pins [package=THT]
  J24 = Screw terminal - 2 pins [package=THT]
  J25 = Screw terminal - 2 pins [package=THT]
  J26 = Screw terminal - 2 pins [package=THT]
  J27 = Screw terminal - 2 pins [package=THT]
  J28 = female pin header, 10 pins [form="♀ (female)"]
  R7 = Rotary Potentiometer (Large) [package=THT]
  R8 = Rotary Potentiometer (Large) [package=THT]
  J29 = double row female pin header, 4 pins [form="♀ (female)"]
  J30 = female pin header, 2 pins [form="♀ (female)"]
  J32 = female pin header, 1 pin [form="♀ (female)"]
  J33 = female pin header, 1 pin [form="♀ (female)"]
  LED1 = LED - 5mm [color="Red (633nm)" package="5 mm [THT]"]
  R9 = Resistor [tolerance=±5% resistance=220 package=THT]

nets:
  N1: U1.PB0, J9.pin2, J18.pin1, J19.pin1, S8.Pin_3, S8.Pin_4
  N2: U1.PB1, J1.pin1, J18.pin2, J19.pin2
  N3: U1.PB2, J1.pin2, J18.pin3, J19.pin3
  N4: U1.PB3, J1.pin3, J18.pin4, J19.pin4
  N5: U1.PB4, J1.pin4, J18.pin5, J19.pin5
  N6: U1.PB5, J1.pin5, J18.pin6, J19.pin6
  N7: U1.PB6, J10.pin2, J18.pin7, J19.pin7, J22.pin4
  N8: U1.PB7, J11.pin2, J18.pin8, J19.pin8, J22.pin3, LED1.anode
  N9: U1.RESET, J1.pin6, J18.pin9, J19.pin9
  N10: U1.VCC, J1.pin7, J18.pin10, J19.pin10
  N11: U1.GND#10, J1.pin8, J18.pin11, J19.pin11
  N12: U1.XTAL2, J1.pin9, J18.pin12, J19.pin12
  N13: U1.XTAL1, J1.pin10, J18.pin13, J19.pin13
  N14: U1.PD0, J18.pin14, J19.pin14, J30.pin2
  N15: U1.PD1, J18.pin15, J19.pin15
  N16: U1.PD2, J18.pin16, J19.pin16
  N17: U1.PD3, J18.pin17, J19.pin17
  N18: U1.PD4, J18.pin18, J19.pin18
  N19: U1.PD5, J18.pin19, J19.pin19
  N20: U1.PD6, J18.pin20, J19.pin20
  N21: U1.PD7, J17.pin20, J20.pin20
  N22: U1.PC0, J17.pin19, J20.pin19
  N23: U1.PC1, J17.pin18, J20.pin18
  N24: U1.PC2, J17.pin17, J20.pin17
  N25: U1.PC3, J17.pin16, J20.pin16
  N26: U1.PC4, J17.pin15, J20.pin15
  N27: U1.PC5, J17.pin14, J20.pin14
  N28: U1.PC6, J17.pin13, J20.pin13
  N29: U1.PC7, J12.pin2, J17.pin12, J20.pin12
  N30: U1.AVCC, J13.pin2, J17.pin11, J20.pin11
  N31: U1.GND#30, J14.pin2, J17.pin10, J20.pin10
  N32: U1.AREF, J17.pin9, J20.pin9
  N33: U1.PA7, J17.pin8, J20.pin8
  N34: U1.PA6, J17.pin7, J20.pin7
  N35: U1.PA5, J17.pin6, J20.pin6
  N36: U1.PA4, J17.pin5, J20.pin5
  N37: U1.PA3, J17.pin4, J20.pin4
  N38: U1.PA2, J17.pin3, J20.pin3
  N39: U1.PA1, J17.pin2, J20.pin2, J29.pin2
  N40: U1.PA0, J17.pin1, J20.pin1, J29.pin1
  GND: U2.VSS, U2.R_W, U2.K, D1.J_C, D1.I_C, D1.H_C, D1.G_C, D1.F_C, D1.E_C, D1.D_C, D1.C_C, D1.B_C, D1.A_C, D7.anode, D8.anode, C2.-, U3.GND, U4.GND, R1.leg1, R2.leg1, J7.pin1, J7.pin2, J7.pin3, J7.pin4, J7.pin5, J7.pin6, J7.pin7, J7.pin8, J7.pin9, J7.pin10, J7.pin11, J7.pin12, J7.pin13, J7.pin14, J7.pin15, J7.pin16, J7.pin17, J7.pin18, J7.pin19, J7.pin20, J15.pin1, J15.pin12, J15.pin16, R3.Pin_0, R4.Pin_0, R5.Pin_0, J22.pin2, R7.leg2, R8.leg2, J32.pin1
  N41: U2.VDD, U3.output_voltage, U4.output_voltage, R1.leg2, R2.leg2, J8.pin1, J8.pin2, J8.pin3, J8.pin4, J8.pin5, J8.pin6, J8.pin7, J8.pin8, J8.pin9, J8.pin10, J8.pin11, J8.pin12, J8.pin13, J8.pin14, J8.pin15, J8.pin16, J8.pin17, J8.pin18, J8.pin19, J8.pin20, J15.pin15, S4.Pin_3, S4.Pin_4, S5.Pin_3, S5.Pin_4, S6.Pin_3, S6.Pin_4, S7.Pin_3, S7.Pin_4, J22.pin1, R7.leg1, R8.leg1, R9.Pin_1
  N42: U2.VO, R2.wiper, J15.pin14
  N43: U2.RS, J15.pin13
  N44: U2.E, J15.pin11
  N45: U2.DB0, J15.pin10
  N46: U2.DB1, J15.pin9
  N47: U2.DB2, J15.pin8
  N48: U2.DB3, J15.pin7
  N49: U2.DB4, J15.pin6
  N50: U2.DB5, J15.pin5
  N51: U2.DB6, J15.pin4
  N52: U2.DB7, J15.pin3
  N53: U2.A, R1.wiper, J15.pin2
  N54: D1.A_A, J2.pin10
  N55: D1.B_A, J2.pin9
  N56: D1.C_A, J2.pin8
  N57: D1.D_A, J2.pin7
  N58: D1.E_A, J2.pin6
  N59: D1.F_A, J2.pin5
  N60: D1.G_A, J2.pin4
  N61: D1.H_A, J2.pin3
  N62: D1.I_A, J2.pin2
  N63: D1.J_A, J2.pin1
  N64: D5.cathode, D6.cathode, C2.+, J6.pin2
  N65: D5.anode, D8.cathode, J5.pin1
  N66: D6.anode, D7.cathode, J5.pin2
  N67: U3.input_voltage, J6.pin3
  N68: U4.input_voltage, J6.pin1
  N69: J9.pin1, J21.2
  N70: J10.pin1, J21.5
  N71: J11.pin1, J21.1
  N72: J12.pin1, J21.3
  N73: J13.pin1, J21.6
  N74: J14.pin1, J21.4
  N75: S4.Pin_1, S4.Pin_2, R3.Pin_1, J16.pin4
  N76: S5.Pin_1, S5.Pin_2, R4.Pin_1, J16.pin3
  N77: S6.Pin_1, S6.Pin_2, R5.Pin_1, J16.pin2
  N78: S7.Pin_1, S7.Pin_2, R6.Pin_1, J16.pin1
  N79: R6.Pin_0, S8.Pin_1, S8.Pin_2
  N80: J23.pin1, J28.pin2
  N81: J23.pin2, J28.pin1
  N82: J24.pin1, J28.pin4
  N83: J24.pin2, J28.pin3
  N84: J25.pin1, J28.pin6
  N85: J25.pin2, J28.pin5
  N86: J26.pin1, J28.pin8
  N87: J26.pin2, J28.pin7
  N88: J27.pin1, J28.pin10
  N89: J27.pin2, J28.pin9
  N90: R7.wiper, J29.pin3
  N91: R8.wiper, J29.pin4
  N92: J30.pin1, J33.pin1
  N93: LED1.cathode, R9.Pin_0

notes:
  HOSA AVR Board
  !!! BLBUVZDORNÁ !!!
