# Fritzing sketch id793_awshome_0 (saved by Fritzing 0.9.3b)

parts:
  Raspberry_Pi1 = Raspberry Pi 2
  Receiver = prefix0002
  Transmitter = prefix0000

nets:
  N1: Raspberry_Pi1.GPIO17, Transmitter.connector2
  N2: Raspberry_Pi1.GPIO27, Receiver.connector1
  N3: Raspberry_Pi1.GND, Receiver.connector0, Transmitter.connector3
  N4: Raspberry_Pi1.5V, Receiver.connector2, Transmitter.connector1

notes:
  Optional Antenna
