# Fritzing sketch id794_B_Daman_Speedometer_0 (saved by Fritzing 0.9.0b)
breadboards: 1

parts:
  Part2 = Arduino Uno (Rev3)
  LCD1 = LCD screen
  LED2 = LED - 5mm [color="Red (633nm)" package="5 mm [THT]"]
  R1 = Trimmer Potentiometer [maximum_resistance=10kΩ package=THT]
  R2 = Photocell (LDR) [package=THT]
  R3 = Resistor [tolerance=±5% resistance=16k package=THT]
  R5 = Resistor [tolerance=±5% resistance=16k package=THT]
  S1 = Pushbutton [package="[THT]"]

nets (from the breadboard view):
  N1: Part2.A0, R2.pin_1, R3.Pin_0
  N2: Part2.A5/SCL, R5.Pin_1, S1.Pin_3, S1.Pin_4
  N3: Part2.D11_PWM/MOSI, LCD1.E
  N4: Part2.D12/MISO, LCD1.RS
  N5: Part2.D13/SCK, LED2.anode
  GND: Part2.GND, LCD1.VSS, LCD1.R/W, LED2.cathode, R1.leg1, R3.Pin_1, R5.Pin_0
  N6: Part2.D2, LCD1.DB7
  N7: Part2.D3_PWM, LCD1.DB6
  N8: Part2.D4, LCD1.DB5
  N9: Part2.D5_PWM, LCD1.DB4
  5V: Part2.5V, LCD1.VDD, R1.leg2, R2.pin_0, S1.Pin_1, S1.Pin_2
  N10: LCD1.V0, R1.wiper

notes:
  Photosensor (left) trips as marble passes through light beam, push switch (right) triggers when marble hits wall at back of speedometer.
