# Fritzing sketch id796_BA1404_FM_Transmitter_0 (saved by Fritzing 0.9.3b)
circuit board: 8cm x 4cm
breadboards: 1

parts:
  IC1 = IC, DIP package, 18 pins [chip_label=IC]
  TRS1 = Audio Jack (TRS) 3.5mm [package="4Ucon 08780 [THT]"]
  R1 = Resistor [tolerance=±5% resistance=220 package=THT]
  R2 = Resistor [tolerance=±5% resistance=220 package=THT]
  C1 = Capacitor [package=cap-pth-small2]
  C2 = Capacitor [package=cap-pth-small2]
  C3 = Electrolytic Capacitor [capacitance=1µF package="100 mil [THT, electrolytic]"]
  C4 = Electrolytic Capacitor [capacitance=1µF package="100 mil [THT, electrolytic]"]
  R3 = Resistor [tolerance=±5% resistance=220 package=THT]
  R4 = Resistor [tolerance=±5% resistance=220 package=THT]
  R5 = Resistor [tolerance=±5% resistance=220 package=THT]
  C5 = Capacitor [package=cap-pth-small2]
  C6 = Electrolytic Capacitor [capacitance=1µF package="100 mil [THT, electrolytic]"]
  R6 = Resistor [tolerance=±5% resistance=220 package=THT]
  C7 = Capacitor [package=cap-pth-small2]
  C8 = Capacitor [package=cap-pth-small2]
  1nF = Capacitor [package=cap-pth-small2]
  C10 = Capacitor [package=cap-pth-small2]
  C11 = Capacitor [package=cap-pth-small2]
  L1 = Inductor [package="400 mil [THT]"]
  C12 = Capacitor [package=cap-pth-small2]
  C13 = Capacitor [package=cap-pth-small2]
  R7 = Resistor [tolerance=±5% resistance=220 package=THT]
  ANT1 = Antenna
  Part1 = Variable Capacitor [capacitance=100nF max_capacitance=10pF min_capacitance=2pF voltage=35V]
  J1 = female pin header, 2 pins [form="♀ (female)"]
  Y1 = CRYSTAL [package=tc26h]
  C14 = Capacitor [package=cap-pth-small2]
  C15 = Capacitor [package=cap-pth-small2]
  C16 = Electrolytic Capacitor [capacitance=1µF package="100 mil [THT, electrolytic]"]

nets:
  N1: IC1.pin1, C4.+
  N2: IC1.pin2, C16.+
  N3: IC1.pin3, IC1.pin8, TRS1.Sleeve, C5.1, 1nF.2, C12.1, J1.pin2, C15.2, C16.-
  N4: IC1.pin4, C15.1
  N5: IC1.pin5, Y1.2
  N6: IC1.pin6, C14.2
  N7: IC1.pin7, C13.1, R7.Pin_1
  N8: IC1.pin9, C11.2, C12.2
  N9: IC1.pin10, C10.2, C11.1, L1.pin_0, Part1.1
  N10: IC1.pin12, C6.+, C7.1, C8.2
  N11: IC1.pin13, R6.Pin_1
  N12: IC1.pin14, R5.Pin_1
  N13: IC1.pin15, R4.Pin_0
  N14: IC1.pin16, R4.Pin_1
  N15: IC1.pin17, R3.Pin_1
  N16: IC1.pin18, C3.+
  N17: TRS1.Ring, R1.Pin_1, C1.2
  N18: TRS1.Tip, R2.Pin_0, C2.1
  N19: R1.Pin_0, C1.1, C3.-
  N20: R2.Pin_1, C2.2, C4.-
  N21: R3.Pin_0, C5.2, C8.1
  N22: R5.Pin_0, C6.-
  N23: R6.Pin_0, C7.2
  N24: 1nF.1, C10.1, L1.pin_1, R7.Pin_0, Part1.2, J1.pin1
  N25: C13.2, ANT1.antenna_lead
  N26: Y1.1, C14.1
