# Fritzing sketch id797_BA4558_0 (saved by Fritzing 0.9.2b)
circuit board: 2.5057cm x 4.8117cm
breadboards: 1

parts:
  DA1 = BA4558 [part_number=BA4558]
  C2 = Electrolytic Capacitor [capacitance=10µF voltage=16V package="200 mil [THT, electrolytic]"]
  C4_0_1mf = Capacitor [package=cap-pth-small-kit]
  C3_0_22mf = Capacitor [package=cap-pth-small-kit]
  R1 = Resistor [tolerance=±5% resistance=10k package="1206 [SMD]"]
  R2 = Resistor [tolerance=±5% resistance=10k package="1206 [SMD]"]
  R3 = Resistor [tolerance=±5% resistance=470k package="1206 [SMD]"]
  R4 = Resistor [tolerance=±5% resistance=10k package="1206 [SMD]"]
  MIC1 = MIC [package=mic_electret_smd]
  C1 = Capacitor [package=cap-pth-small2]
  JP1 = Header 1 [package=1x01_offset]
  C5_0_22mf = Capacitor [package=cap-pth-small-kit]
  JP2 = Header 1 [package=1x01_offset]
  R6 = Resistor [tolerance=±5% resistance=470k package="1206 [SMD]"]
  C7_0_22mf1 = Capacitor [package=ctz3]
  MIC2 = MIC [package=mic_electret_smd]
  R8 = Resistor [tolerance=±5% resistance=10k package="1206 [SMD]"]
  C6 = Electrolytic Capacitor [capacitance=10µF voltage=16V package="200 mil [THT, electrolytic]"]
  R7 = Resistor [tolerance=±5% resistance=10k package="1206 [SMD]"]
  R5 = Resistor [tolerance=±5% resistance=10k package="1206 [SMD]"]
  JP3_+ = Header 1 [package=1x01_offset]
  JP4_- = Header 1 [package=1x01_offset]

nets:
  N1: DA1.connector0, C3_0_22mf.1, R3.Pin_0
  N2: DA1.connector1, R3.Pin_1, C1.1
  N3: DA1.connector2, C2.+, R1.Pin_1, R2.Pin_0, R4.Pin_0
  GND: DA1.connector3, C2.-, C4_0_1mf.1, R2.Pin_1, MIC1.2, MIC2.1, C6.-, R7.Pin_1, JP4_-.1
  N4: DA1.connector4, R8.Pin_0, C6.+, R7.Pin_0, R5.Pin_1
  N5: DA1.connector5, R6.Pin_0, C7_0_22mf1.2
  N6: DA1.connector6, C5_0_22mf.1, R6.Pin_1
  N7: DA1.connector7, C4_0_1mf.2, R4.Pin_1, R5.Pin_0, JP3_+.1
  N8: C3_0_22mf.2, JP1.1
  N9: R1.Pin_0, MIC1.1, C1.2
  N10: C5_0_22mf.2, JP2.1
  N11: C7_0_22mf1.1, MIC2.2, R8.Pin_1
