# Fritzing sketch id798_arduino_motor_servo_shield_0 (saved by Fritzing 0.7.4b)
breadboards: 1

parts:
  IC1 = H-Bridge [package=THT]
  J1 = female pin header, 2 pins [form="♀ (female)"]
  J2 = female pin header, 2 pins [form="♀ (female)"]
  J3 = female pin header, 2 pins [form="♀ (female)"]
  J4 = female pin header, 2 pins [form="♀ (female)"]
  Acc/Gyro = Triple Axis Accelerometer Breakout - ADXL345
  Servo_1 = male pin header, 3 pins [form="♂ (male)"]
  Servo_2 = male pin header, 3 pins [form="♂ (male)"]
  A0-3 = male pin header, 4 pins [form="♂ (male)"]
  5+_G = female pin header, 2 pins [form="♀ (female)"]
  Arduino1 = Arduino

nets:
  N1: IC1.1_2EN, Arduino1.D8
  N2: IC1.1A, Arduino1.D9
  N3: IC1.1Y, J2.pin2, J4.pin2
  GND: IC1.GND1, IC1.GND2, IC1.GND3, IC1.GND4, Acc/Gyro.GND, Servo_1.pin3, Servo_2.pin3, 5+_G.pin2, Arduino1.GND
  N4: IC1.2Y, J2.pin1, J4.pin1
  N5: IC1.2A, Arduino1.D10
  N6: IC1.VCC2, Arduino1.VIN
  N7: IC1.3_4EN, Arduino1.D11
  N8: IC1.3A, Arduino1.D12
  N9: IC1.3Y, J1.pin2, J3.pin2
  N10: IC1.4Y, J1.pin1, J3.pin1
  N11: IC1.4A, Arduino1.D6
  N12: IC1.VCC1, Servo_1.pin2, Servo_2.pin2, 5+_G.pin1, Arduino1.+5V
  VCC: Acc/Gyro.VCC, Arduino1.3V3
  N13: Acc/Gyro.CS, Arduino1.A5
  N14: Acc/Gyro.INT1, Arduino1.A4
  N15: Servo_1.pin1, Arduino1.D5
  N16: Servo_2.pin1, Arduino1.D3
  N17: A0-3.pin1, Arduino1.A3
  N18: A0-3.pin2, Arduino1.A2
  N19: A0-3.pin3, Arduino1.A1
  N20: A0-3.pin4, Arduino1.A0
