# Fritzing sketch id79_Untitled_Sketch_2_0 (saved by Fritzing 0.9.3b)
circuit board: 8.46667cm x 5.64444cm
breadboards: 1

parts:
  Componente2 = Arduino Uno (Rev3)
  RHT1 = Humidity and Temperature Sensor RHT03

nets:
  N1: Componente2.D13/SCK, RHT1.Data-signal
  N2: Componente2.GND, RHT1.GND_2
  5V: Componente2.5V, RHT1.Vcc
