# Fritzing sketch id7_Untitled_Sketch_0 (saved by Fritzing 0.9.3b)
breadboards: 1
stripboards: 4

parts:
  Part1 = Arduino Uno (Rev3)
  Part2 = Bluetooth HC-05 Macho
  ldr = Photocell (LDR) [package=THT]
  LED1 = smd LED [color="Red (633nm)" package="0805 [SMD]"]
  LED2 = smd LED [color="Red (633nm)" package="0805 [SMD]"]
  LED3 = smd LED [color="Red (633nm)" package="0805 [SMD]"]
  LED4 = smd LED [color="Red (633nm)" package="0805 [SMD]"]
  LED5 = smd LED [color="Red (633nm)" package="0805 [SMD]"]
  IC1 = L293D [package=THT]
  M1 = DC Motor
  J2 = Basic Servo
  ph_d_1 = S1133 Si Photodiode [package="8mm Ceramic [THT]"]
  IR = LTR-301 [package=ltr-301]
  R3 = Resistor [tolerance=±5% resistance=220 package=THT]
  R4 = Resistor [tolerance=±5% resistance=220 package=THT]
  R5 = Resistor [tolerance=±5% resistance=220 package=THT]
  R6 = Resistor [tolerance=±5% resistance=220 package=THT]
  R7 = Resistor [tolerance=±5% resistance=10k package=THT]
  R8 = Resistor [tolerance=±5% resistance=20k package=THT]
  R9 = Resistor [tolerance=±5% resistance=220 package=THT]
  J3 = Basic Servo
  R10 = Resistor [tolerance=±5% resistance=220 package=THT]
  IR_2 = LTR-301 [package=ltr-301]
  ph_d_2 = S1133 Si Photodiode [package="8mm Ceramic [THT]"]
  R11 = Resistor [tolerance=±5% resistance=220 package=THT]
  R12 = Resistor [tolerance=±5% resistance=20k package=THT]

nets:
  N1: Part1.A3, ldr.pin_0, R7.Pin_1
  N2: Part1.D8, IC1.In_2
  N3: Part1.D9_PWM, J3.pulse
  N4: Part1.D10_PWM/SS, LED2.anode
  N5: Part1.D11_PWM/MOSI, IC1.In_1
  N6: Part1.D12/MISO, IC1.Enable_1
  N7: Part1.D13/SCK, J2.pulse
  N8: Part1.D0/RX, Part2.TXD
  N9: Part1.D1/TX, Part2.RXD
  N10: Part1.D7, LED1.cathode, LED1.anode, LED3.anode, LED4.anode, LED5.anode, R3.Pin_0
  VCC: Part1.5V, Part2.VCC, ldr.pin_1, IC1.+V, J2.vcc, ph_d_1.anode, IR.C, J3.vcc, IR_2.C, ph_d_2.anode
  GND: Part1.GND, IC1.0V, J2.gnd, R3.Pin_1, R4.Pin_1, R5.Pin_1, R6.Pin_1, R7.Pin_0, R8.Pin_1, R9.Pin_1, J3.gnd, R10.Pin_1, R11.Pin_1, R12.Pin_1
  N11: Part1.VIN, IC1.+Vmotor
  N12: LED2.cathode, R9.Pin_0
  N13: LED3.cathode, R4.Pin_0
  N14: LED4.cathode, R5.Pin_0
  N15: LED5.cathode, R6.Pin_0
  N16: IC1.Out_1_(_Controlled_by_Enable_1_), M1.pin_1
  N17: IC1.Out_2_(_Controlled_by_Enable_1_), M1.pin_2
  N18: ph_d_1.cathode, R8.Pin_0
  N19: IR.E, R10.Pin_0
  N20: IR_2.E, R11.Pin_0
  N21: ph_d_2.cathode, R12.Pin_0
