# Fritzing sketch id802_rgb1_0 (saved by Fritzing 0.3.12b)
breadboards: 1

parts:
  U2 = atmega168 [package="DIP28 [THT]"]
  XTAL1 = Crystal [package=THT]
  R2 = Resistor [resistance=1k package=THT]
  S2 = Pushbutton [package="[THT]"]
  LED2 = green LED - 5mm
  LED3 = Blue LED - 5mm
  R3 = Resistor [resistance=1k package=THT]
  LED1 = Red LED - 5mm
  LED2_2 = green LED - 5mm
  LED3_2 = Blue LED - 5mm
  LED1_2 = Red LED - 5mm
  LED2_3 = green LED - 5mm
  LED3_3 = Blue LED - 5mm
  LED1_3 = Red LED - 5mm
  LED2_4 = green LED - 5mm
  LED3_4 = Blue LED - 5mm
  LED1_4 = Red LED - 5mm
  C2 = Electrolytic Capacitor [package=THT]
  VCC1 = obsolete Battery
  S3 = Toggle Switch [package=THT]
  D1 = Rectifier Diode [package=THT]
  R4 = Resistor [resistance=330 package=THT]
  R3_2 = Resistor [resistance=1k package=THT]
  R3_3 = Resistor [resistance=1k package=THT]
  R3_4 = Resistor [resistance=1k package=THT]

nets:
  N1: U2.Pin_1, R2.Pin_1
  N2: U2.Pin_2, LED1_3.cathode
  N3: U2.Pin_3, LED2_4.cathode
  N4: U2.Pin_4, LED3_4.cathode
  N5: U2.Pin_5, LED1_2.cathode
  N6: U2.Pin_6, LED2_3.cathode
  N7: U2.Pin_7, U2.Pin_20, R2.Pin_0, R3.Pin_0, C2.+, D1.cathode, R4.Pin_0, R3_2.Pin_0, R3_3.Pin_0, R3_4.Pin_0
  N8: U2.Pin_8, U2.Pin_22, S2.Pin_3, S2.Pin_4, C2.-, VCC1.-
  N9: U2.Pin_9, XTAL1.pin_0
  N10: U2.Pin_10, XTAL1.pin_1
  N11: U2.Pin_11, LED3_3.cathode
  N12: U2.Pin_12, LED1.cathode
  N13: U2.Pin_13, LED2_2.cathode
  N14: U2.Pin_14, LED3_2.cathode
  N15: U2.Pin_15, LED1_4.cathode
  N16: U2.Pin_16, LED2.cathode
  N17: U2.Pin_17, LED3.cathode
  N18: U2.Pin_18, S2.Pin_1, S2.Pin_2, R4.Pin_1
  N19: LED2.anode, LED3.anode, LED1_4.anode, R3_3.Pin_1
  N20: R3.Pin_1, LED1_3.anode, LED2_4.anode, LED3_4.anode
  N21: LED1.anode, LED2_2.anode, LED3_2.anode, R3_2.Pin_1
  N22: LED1_2.anode, LED2_3.anode, LED3_3.anode, R3_4.Pin_1
  N23: VCC1.+, S3.COM
  N24: S3.L2, D1.anode

notes:
  3--5V
  Ch a
  Ch b
  Ch c
  Ch d
