# Fritzing sketch id803_BasicBlink_0 (saved by Fritzing 0.9.2b)
breadboards: 1

parts:
  Part1 = Arduino Uno (Rev3)
  LED1 = LED - 5mm [color="Red (633nm)" package="5 mm [THT]"]
  LED2 = LED - 5mm [color="Green (565nm)" package="5 mm [THT]"]
  R1 = Resistor [tolerance=±5% resistance=220 package=THT]
  R2 = Resistor [tolerance=±5% resistance=220 package=THT]

nets:
  N1: Part1.D11_PWM/MOSI, R2.Pin_1
  N2: Part1.D13/SCK, R1.Pin_1
  N3: Part1.GND, LED1.cathode, LED2.cathode
  N4: LED1.anode, R1.Pin_0
  N5: LED2.anode, R2.Pin_0

notes:
  Step 1
  Attach the GND - pin to the breadboard
  Attach the 5V pin + to the breadboard
  this will power the 2 rails along the edge of the board
  The long leg of the LED is positive +
  The short leg is negative -
  Use a 220Ω resistor for each LED
  Connect 1 LED to pin 13 and the other to pin 11
