# Fritzing sketch id804_BasicCircuit_0 (saved by Fritzing 0.9.2b)
breadboards: 1

parts:
  R1 = Resistor [tolerance=±5% resistance=470 package=THT]
  R3 = Resistor [tolerance=±5% resistance=270 package=THT]
  LED1 = LED - 5mm [color="Red (633nm)" package="5 mm [THT]"]
  LED2 = LED - 5mm [color="Green (565nm)" package="5 mm [THT]"]
  S1 = Pushbutton [package="[THT]"]
  VCC1 = Battery

nets:
  N1: R1.Pin_0, R3.Pin_0, S1.Pin_1, S1.Pin_2
  N2: R1.Pin_1, LED1.cathode
  N3: R3.Pin_1, LED2.cathode
  N4: LED1.anode, LED2.anode, VCC1.-, VCC1.+
  N5: S1.Pin_3, S1.Pin_4
