# Fritzing sketch id805_attinyboard (saved by Fritzing 0.6.5b)
breadboards: 1

parts:
  IC1 = IC, DIP package, 8 pins [chip_label=IC spacing=300mil]
  J3 = shrouded pin header, 8 pins [form="♂ (shrouded male)"]
  J1 = female pin header, 4 pins [form="♀ (female)"]

nets:
  N1: IC1.pin1, J3.pin3, J1.pin3
  N2: IC1.pin2, J3.pin5, J1.pin4
  N3: IC1.pin3, J3.pin6
  N4: IC1.pin4, J3.pin4, J1.pin2
  N5: IC1.pin5, J3.pin7
  N6: IC1.pin8, J3.pin2, J1.pin1

notes:
  p1
  -
