# Fritzing sketch id807_ResistorCapacitor_Network2parts_0 (saved by Fritzing 0.9.3b)
breadboards: 1

parts:
  R1 = Resistor [tolerance=±5% resistance=4.7k package=THT]
  R2 = Resistor [tolerance=±5% resistance=470 package=THT]
  R3 = Resistor [tolerance=±5% resistance=470 package=THT]
  R4 = Resistor [tolerance=±5% resistance=4.7k package=THT]
  R5 = Resistor [tolerance=±5% resistance=470 package=THT]
  R6 = Resistor [tolerance=±5% resistance=470 package=THT]
  C1 = Ceramic Capacitor [capacitance=3.3µF package="100 mil [THT, multilayer]"]
  C2 = Ceramic Capacitor [capacitance=3.3µF package="100 mil [THT, multilayer]"]
  C3 = Ceramic Capacitor [capacitance=220µF package="100 mil [THT, multilayer]"]
  LED1 = LED - 5mm [color="Red (633nm)" package="5 mm [THT]"]
  VCC1 = Battery block 9V
  Q1 = NPN-Transistor [part_number=2N2222 package="TO92 [THT]"]
  Q2 = NPN-Transistor [part_number=2N2222 package="TO92 [THT]"]
  Q3 = NPN-Transistor [part_number=2N2222 package="TO92 [THT]"]
  R7 = Resistor [tolerance=±5% resistance=100k package=THT]

nets:
  N1: R1.Pin_1, C1.0, Q1.C, R7.Pin_1
  N2: R2.Pin_1, C1.1, Q2.B
  N3: R3.Pin_1, C2.0, Q1.B
  N4: R4.Pin_1, C2.1, Q2.C
  N5: R5.Pin_0, Q3.E
  N6: R5.Pin_1, R6.Pin_0, C3.0
  N7: R6.Pin_1, LED1.anode
  N8: C3.1, LED1.cathode, VCC1.-, Q1.E
  N9: VCC1.+, Q3.C
  N10: Q3.B, R7.Pin_0
