# Fritzing sketch id808_ResistorCapacitor_Network3parts_0 (saved by Fritzing 0.9.3b)
circuit board: 3.3632cm x 5.8298cm
breadboards: 1

parts:
  Q3 = NPN-Transistor [part_number=2N2222 package="TO92 [THT]"]
  Q2 = NPN-Transistor [part_number=2N2222 package="TO92 [THT]"]
  LED1 = LED - 5mm [color="Red (633nm)" package="5 mm [THT]"]
  C2 = Ceramic Capacitor [capacitance=3.3µF package="100 mil [THT, multilayer]"]
  R6 = Resistor [tolerance=±5% resistance=470 package=THT]
  R2 = Resistor [tolerance=±5% resistance=470 package=THT]
  R1 = Resistor [tolerance=±5% resistance=4.7k package=THT]
  R7 = Resistor [tolerance=±5% resistance=100k package=THT]
  R3 = Resistor [tolerance=±5% resistance=470 package=THT]
  C3 = Ceramic Capacitor [capacitance=100nF voltage=16V package="100 mil [THT, multilayer]"]
  C1 = Ceramic Capacitor [capacitance=3.3µF package="100 mil [THT, multilayer]"]
  R5 = Resistor [tolerance=±5% resistance=470 package=THT]
  R4 = Resistor [tolerance=±5% resistance=4.7k package=THT]
  VCC1 = Battery block 9V
  Q1 = NPN-Transistor [part_number=2N2222 package="TO92 [THT]"]

nets:
  N1: Q3.E, R5.Pin_0
  N2: Q3.B, R7.Pin_0
  N3: Q3.C, R2.Pin_0, R1.Pin_0, R3.Pin_0, R4.Pin_0, VCC1.+
  N4: Q2.E, LED1.cathode, C3.1, VCC1.-, Q1.E
  N5: Q2.B, R2.Pin_1, C1.1
  N6: Q2.C, C2.1, R4.Pin_1
  N7: LED1.anode, R6.Pin_1
  N8: C2.0, R3.Pin_1, Q1.B
  N9: R6.Pin_0, C3.0, R5.Pin_1
  N10: R1.Pin_1, R7.Pin_1, C1.0, Q1.C
