# Fritzing sketch id80_LED_matrix_driver___2_layer_print_final_0 (saved by Fritzing 0.9.0b)
circuit board: 7.57438cm x 6.46762cm
perfboards: 1

parts:
  CD4017 = IC, DIP package, 16 pins [chip_label=CD4017]
  J1 = female pin header, 7 pins [form="♀ (female)"]
  Q6 = PNP-Transistor [package="TO92 [THT]"]
  Q2 = PNP-Transistor [package="TO92 [THT]"]
  Q1 = PNP-Transistor [package="TO92 [THT]"]
  Q3 = PNP-Transistor [package="TO92 [THT]"]
  Q7 = PNP-Transistor [package="TO92 [THT]"]
  Q8 = PNP-Transistor [package="TO92 [THT]"]
  Q4 = PNP-Transistor [package="TO92 [THT]"]
  Q5 = PNP-Transistor [package="TO92 [THT]"]
  R6 = Resistor [tolerance=±5% resistance=1k package=THT]
  R2 = Resistor [tolerance=±5% resistance=1k package=THT]
  R1 = Resistor [tolerance=±5% resistance=1k package=THT]
  R3 = Resistor [tolerance=±5% resistance=1k package=THT]
  R7 = Resistor [tolerance=±5% resistance=1k package=THT]
  R8 = Resistor [tolerance=±5% resistance=1k package=THT]
  R4 = Resistor [tolerance=±5% resistance=1k package=THT]
  R5 = Resistor [tolerance=±5% resistance=1k package=THT]
  J2 = female pin header, 1 pin [form="♀ (female)"]
  J3 = female pin header, 1 pin [form="♀ (female)"]
  J4 = female pin header, 1 pin [form="♀ (female)"]
  J5 = female pin header, 1 pin [form="♀ (female)"]
  J6 = female pin header, 1 pin [form="♀ (female)"]
  J7 = female pin header, 1 pin [form="♀ (female)"]
  J8 = female pin header, 1 pin [form="♀ (female)"]
  J9 = female pin header, 1 pin [form="♀ (female)"]
  J10 = female pin header, 1 pin [form="♀ (female)"]
  SN74HC596 = IC, DIP package, 16 pins [chip_label=SN74HC596]
  SN74HC595 = IC, DIP package, 16 pins [chip_label=SN74HC596]
  R9 = Resistor [tolerance=±5% resistance=150 package=THT]
  J11 = female pin header, 1 pin [form="♀ (female)"]
  R10 = Resistor [tolerance=±5% resistance=150 package=THT]
  R11 = Resistor [tolerance=±5% resistance=150 package=THT]
  R12 = Resistor [tolerance=±5% resistance=150 package=THT]
  R13 = Resistor [tolerance=±5% resistance=150 package=THT]
  R14 = Resistor [tolerance=±5% resistance=150 package=THT]
  R15 = Resistor [tolerance=±5% resistance=150 package=THT]
  R16 = Resistor [tolerance=±5% resistance=150 package=THT]
  R17 = Resistor [tolerance=±5% resistance=150 package=THT]
  R18 = Resistor [tolerance=±5% resistance=150 package=THT]
  R19 = Resistor [tolerance=±5% resistance=150 package=THT]
  R20 = Resistor [tolerance=±5% resistance=150 package=THT]
  R21 = Resistor [tolerance=±5% resistance=150 package=THT]
  R22 = Resistor [tolerance=±5% resistance=150 package=THT]
  R23 = Resistor [tolerance=±5% resistance=150 package=THT]
  R24 = Resistor [tolerance=±5% resistance=150 package=THT]
  R25 = Resistor [tolerance=±5% resistance=150 package=THT]
  R26 = Resistor [tolerance=±5% resistance=150 package=THT]
  R27 = Resistor [tolerance=±5% resistance=150 package=THT]
  R28 = Resistor [tolerance=±5% resistance=150 package=THT]
  R29 = Resistor [tolerance=±5% resistance=150 package=THT]
  R30 = Resistor [tolerance=±5% resistance=150 package=THT]
  R31 = Resistor [tolerance=±5% resistance=150 package=THT]
  R32 = Resistor [tolerance=±5% resistance=150 package=THT]
  J12 = female pin header, 1 pin [form="♀ (female)"]
  J13 = female pin header, 1 pin [form="♀ (female)"]
  J14 = female pin header, 1 pin [form="♀ (female)"]
  J15 = female pin header, 1 pin [form="♀ (female)"]
  J16 = female pin header, 1 pin [form="♀ (female)"]
  J17 = female pin header, 1 pin [form="♀ (female)"]
  J18 = female pin header, 1 pin [form="♀ (female)"]
  J19 = female pin header, 1 pin [form="♀ (female)"]
  J20 = female pin header, 1 pin [form="♀ (female)"]
  J21 = female pin header, 1 pin [form="♀ (female)"]
  J22 = female pin header, 1 pin [form="♀ (female)"]
  J23 = female pin header, 1 pin [form="♀ (female)"]
  J24 = female pin header, 1 pin [form="♀ (female)"]
  J25 = female pin header, 1 pin [form="♀ (female)"]
  J26 = female pin header, 1 pin [form="♀ (female)"]
  J27 = female pin header, 1 pin [form="♀ (female)"]
  J28 = female pin header, 1 pin [form="♀ (female)"]
  J29 = female pin header, 1 pin [form="♀ (female)"]
  SN74HC597 = IC, DIP package, 16 pins [chip_label=SN74HC596]
  J30 = female pin header, 1 pin [form="♀ (female)"]
  J31 = female pin header, 1 pin [form="♀ (female)"]
  J32 = female pin header, 1 pin [form="♀ (female)"]
  J33 = female pin header, 1 pin [form="♀ (female)"]
  J34 = female pin header, 1 pin [form="♀ (female)"]
  J35 = female pin header, 1 pin [form="♀ (female)"]
  J36 = female pin header, 1 pin [form="♀ (female)"]
  J37 = female pin header, 1 pin [form="♀ (female)"]
  J38 = female pin header, 1 pin [form="♀ (female)"]
  J39 = female pin header, 1 pin [form="♀ (female)"]
  J40 = female pin header, 1 pin [form="♀ (female)"]
  J41 = female pin header, 1 pin [form="♀ (female)"]
  J42 = female pin header, 1 pin [form="♀ (female)"]
  J43 = female pin header, 1 pin [form="♀ (female)"]
  J44 = female pin header, 1 pin [form="♀ (female)"]
  J45 = female pin header, 1 pin [form="♀ (female)"]
  J46 = female pin header, 1 pin [form="♀ (female)"]
  J47 = female pin header, 1 pin [form="♀ (female)"]
  J48 = female pin header, 1 pin [form="♀ (female)"]
  J49 = female pin header, 1 pin [form="♀ (female)"]
  J50 = female pin header, 1 pin [form="♀ (female)"]
  J51 = female pin header, 1 pin [form="♀ (female)"]
  J52 = female pin header, 1 pin [form="♀ (female)"]
  J53 = female pin header, 1 pin [form="♀ (female)"]
  J54 = female pin header, 1 pin [form="♀ (female)"]
  J55 = female pin header, 1 pin [form="♀ (female)"]
  J56 = female pin header, 1 pin [form="♀ (female)"]

nets:
  N1: CD4017.pin1, R6.Pin_1
  N2: CD4017.pin2, R2.Pin_1
  N3: CD4017.pin3, R1.Pin_1
  N4: CD4017.pin4, R3.Pin_1
  N5: CD4017.pin5, R7.Pin_1
  N6: CD4017.pin6, R8.Pin_1
  N7: CD4017.pin7, R4.Pin_1
  N8: CD4017.pin8, CD4017.pin13, J1.pin1, Q6.E, Q2.E, Q1.E, Q3.E, Q7.E, Q8.E, Q4.E, Q5.E, SN74HC596.pin8, SN74HC596.pin13, SN74HC595.pin8, SN74HC595.pin13, J18.pin1, J19.pin1, J20.pin1, J21.pin1, J22.pin1, J23.pin1, J24.pin1, J25.pin1, J26.pin1, J27.pin1, J28.pin1, J29.pin1, SN74HC597.pin8, SN74HC597.pin13
  N9: CD4017.pin10, R5.Pin_1
  N10: CD4017.pin14, J1.pin2
  N11: CD4017.pin15, J1.pin3
  N12: CD4017.pin16, J1.pin4, J2.pin1, SN74HC596.pin10, SN74HC596.pin16, SN74HC595.pin10, SN74HC595.pin16, J12.pin1, J13.pin1, J14.pin1, J15.pin1, J16.pin1, J17.pin1, SN74HC597.pin10, SN74HC597.pin16
  N13: J1.pin5, SN74HC596.pin11, SN74HC595.pin11, SN74HC597.pin11
  N14: J1.pin6, SN74HC596.pin12, SN74HC595.pin12, SN74HC597.pin12, J53.pin1, J54.pin1, J55.pin1, J56.pin1
  N15: J1.pin7, SN74HC595.pin14
  N16: Q6.B, R6.Pin_0
  N17: Q6.C, J3.pin1
  N18: Q2.B, R2.Pin_0
  N19: Q2.C, J5.pin1
  N20: Q1.B, R1.Pin_0
  N21: Q1.C, J4.pin1
  N22: Q3.B, R3.Pin_0
  N23: Q3.C, J6.pin1
  N24: Q7.B, R7.Pin_0
  N25: Q7.C, J7.pin1
  N26: Q8.B, R8.Pin_0
  N27: Q8.C, J8.pin1
  N28: Q4.B, R4.Pin_0
  N29: Q4.C, J10.pin1
  N30: Q5.B, R5.Pin_0
  N31: Q5.C, J9.pin1
  N32: SN74HC596.pin1, R18.Pin_0
  N33: SN74HC596.pin2, R19.Pin_0
  N34: SN74HC596.pin3, R20.Pin_0
  N35: SN74HC596.pin4, R21.Pin_0
  N36: SN74HC596.pin5, R22.Pin_0
  N37: SN74HC596.pin6, R23.Pin_0
  N38: SN74HC596.pin7, R24.Pin_0
  N39: SN74HC596.pin9, SN74HC597.pin14
  N40: SN74HC596.pin14, SN74HC595.pin9
  N41: SN74HC596.pin15, R17.Pin_0
  N42: SN74HC595.pin1, R10.Pin_0
  N43: SN74HC595.pin2, R11.Pin_0
  N44: SN74HC595.pin3, R12.Pin_0
  N45: SN74HC595.pin4, R13.Pin_0
  N46: SN74HC595.pin5, R14.Pin_0
  N47: SN74HC595.pin6, R15.Pin_0
  N48: SN74HC595.pin7, R16.Pin_0
  N49: SN74HC595.pin15, R9.Pin_0
  N50: R9.Pin_1, J11.pin1
  N51: R10.Pin_1, J30.pin1
  N52: R11.Pin_1, J31.pin1
  N53: R12.Pin_1, J32.pin1
  N54: R13.Pin_1, J33.pin1
  N55: R14.Pin_1, J34.pin1
  N56: R15.Pin_1, J35.pin1
  N57: R16.Pin_1, J36.pin1
  N58: R17.Pin_1, J37.pin1
  N59: R18.Pin_1, J38.pin1
  N60: R19.Pin_1, J39.pin1
  N61: R20.Pin_1, J40.pin1
  N62: R21.Pin_1, J41.pin1
  N63: R22.Pin_1, J42.pin1
  N64: R23.Pin_1, J43.pin1
  N65: R24.Pin_1, J44.pin1
  N66: R25.Pin_0, SN74HC597.pin15
  N67: R25.Pin_1, J45.pin1
  N68: R26.Pin_0, SN74HC597.pin1
  N69: R26.Pin_1, J46.pin1
  N70: R27.Pin_0, SN74HC597.pin2
  N71: R27.Pin_1, J47.pin1
  N72: R28.Pin_0, SN74HC597.pin3
  N73: R28.Pin_1, J48.pin1
  N74: R29.Pin_0, SN74HC597.pin4
  N75: R29.Pin_1, J49.pin1
  N76: R30.Pin_0, SN74HC597.pin5
  N77: R30.Pin_1, J50.pin1
  N78: R31.Pin_0, SN74HC597.pin6
  N79: R31.Pin_1, J51.pin1
  N80: R32.Pin_0, SN74HC597.pin7
  N81: R32.Pin_1, J52.pin1

notes:
  Columns  8----------------------1
  Wire Key:
  Blue-Bottom holes solder path
  Green- Jumper
  Yellow- Wires out to matrix
  Red- Wires to Arduino
  Pin 11
  Pin 10
  Pin 13
  Vcc+ 5V
  Pin 08
  Pin 09
  Ground Pin
  Row 6
  Row 2
  Row 1
  Row 3
  Row 7
  Row 8
  Row 4
  Row 5
