# Fritzing sketch id810_Experiment_1_0 (saved by Fritzing 0.7.11b)
breadboards: 1

parts:
  IC1 = IC, DIP package, 16 pins [chip_label=WTV020-SD]
  Arduino1 = Arduino
  R1 = 470 Ω Resistor [package=THT]
  LED1 = white smd LED [package="0603 [SMD]"]
  S2 = Pushbutton [package="[THT]"]
  S1 = Pushbutton [package="[THT]"]
  SPKR1 = Loudspeaker

nets:
  N1: IC1.pin1, Arduino1.D2
  N2: IC1.pin4, SPKR1.pin2
  N3: IC1.pin5, SPKR1.pin1
  N4: IC1.pin7, Arduino1.D3
  N5: IC1.pin8, Arduino1.GND, S2.Pin_1, S2.Pin_2, S1.Pin_1, S1.Pin_2
  N6: IC1.pin10, Arduino1.D4
  N7: IC1.pin12, S2.Pin_3, S2.Pin_4
  N8: IC1.pin13, S1.Pin_3, S1.Pin_4
  N9: IC1.pin15, Arduino1.D5, LED1.cathode
  N10: IC1.pin16, Arduino1.3V3, R1.Pin_1
  N11: R1.Pin_0, LED1.anode

notes:
  1
  16
  8
  9
  Duemilanove
  NEXT
  PREV
