# Fritzing sketch id814_Basic_Pushbutton_LED_0 (saved by Fritzing 0.9.2b)
breadboards: 1

parts:
  R1 = Resistor [tolerance=±5% resistance=220 package=THT]
  LED1 = LED - 5mm [color="Red (633nm)" package="5 mm [THT]"]
  S1 = Pushbutton [package=THT]

nets:
  N1: R1.Pin_0, LED1.anode
  N2: R1.Pin_1, S1.leg0, S1.leg1
  GND: LED1.cathode
