# Fritzing sketch id817_Basic_Multi_Blink_0 (saved by Fritzing 0.9.0b)
breadboards: 1

parts:
  LED1 = LED - 5mm [color="Red (633nm)" package="5 mm [THT]"]
  R1 = Resistor [tolerance=±5% resistance=220 package=THT]
  Part1 = Arduino Uno (Rev3)
  LED2 = LED - 5mm [color="Blue (525nm)" package="5 mm [THT]"]
  LED3 = LED - 5mm [color="Green (560nm)" package="5 mm [THT]"]
  LED4 = LED - 5mm [color="Yellow (585nm)" package="5 mm [THT]"]
  R2 = Resistor [tolerance=±5% resistance=220 package=THT]
  R3 = Resistor [tolerance=±5% resistance=220 package=THT]
  R4 = Resistor [tolerance=±5% resistance=220 package=THT]

nets:
  N1: LED1.cathode, R1.Pin_1
  N2: LED1.anode, Part1.D13/SCK
  N3: R1.Pin_0, Part1.5V, R2.Pin_0, R3.Pin_0, R4.Pin_0
  N4: Part1.D10_PWM/SS, LED4.anode
  N5: Part1.D11_PWM/MOSI, LED3.anode
  N6: Part1.D12/MISO, LED2.anode
  N7: LED2.cathode, R2.Pin_1
  N8: LED3.cathode, R3.Pin_1
  N9: LED4.cathode, R4.Pin_1
