# Fritzing sketch id818_Basic_Pot_pwmLED_0 (saved by Fritzing 0.9.0b)
breadboards: 1

parts:
  Part1 = Arduino Uno (Rev3) - ICSP
  LED1 = LED - 5mm [color="Red (633nm)" package="5 mm [THT]"]
  R1 = Resistor [tolerance=±5% resistance=220 package=THT]
  R2 = Rotary Potentiometer (Small) [maximum_resistance=100kΩ package=THT]

nets:
  N1: Part1.A0, R2.wiper
  N2: Part1.D6_PWM, LED1.anode
  N3: Part1.5V, R2.leg1
  N4: Part1.GND, R1.Pin_0, R2.leg2
  N5: LED1.cathode, R1.Pin_1
