# Fritzing sketch id819_basic_push_button_0 (saved by Fritzing 0.9.0b)

parts:
  パーツ1 = Arduino Uno (Rev3) - ICSP
  S1 = Round Pushbutton

nets:
  N1: パーツ1.ICSP_MISO, パーツ1.D12/MISO, S1.leg0
  N2: パーツ1.GND, S1.leg1
