# Fritzing sketch id820_basic_push_button_circuit_1_0 (saved by Fritzing 0.9.0b)
breadboards: 1

parts:
  LED1 = LED - 5mm [color="Red (633nm)" package="5 mm [THT]"]
  S1 = Pushbutton [package="[THT]"]
  R1 = Resistor [tolerance=±5% resistance=560 package=THT]  # not connected
  BAT1 = Battery Holders [package=battcom_20mm_pth]

nets:
  N1: LED1.anode, S1.Pin_1, S1.Pin_2
  N2: S1.Pin_3, S1.Pin_4, BAT1.+
