# Fritzing sketch id821_Act_3_0 (saved by Fritzing 0.9.3b)
breadboards: 1

parts:
  Part1 = Arduino Uno (Rev3)
  LED1 = 7-SEGMENT-4DIGIT-YOUNGSUN [package=7-segment-4digit-youngsun-longpads]
  R1 = Resistor [tolerance=±5% resistance=10k package=THT]
  R2 = Resistor [tolerance=±5% resistance=10k package=THT]
  LED2 = LED - 5mm [color="Red (633nm)" package="5 mm [THT]"]
  R3 = Resistor [tolerance=±5% resistance=10k package=THT]
  S2 = Momentary Switch [package=tactile_switch_smd]
  S3 = Momentary Switch [package=tactile_switch_smd]
  J1 = Piezo Speaker

nets:
  N1: Part1.A0, LED1.DP
  N2: Part1.A2, LED1.DIG2
  N3: Part1.A4/SDA, LED1.DIG4
  N4: Part1.A5/SCL, R3.Pin_1
  N5: Part1.D8, LED1.G
  N6: Part1.D9_PWM, J1.pin2
  N7: Part1.D10_PWM/SS, LED1.DIG1
  N8: Part1.D11_PWM/MOSI, LED1.DIG3
  N9: Part1.D12/MISO, R1.Pin_0, S2.1
  N10: Part1.D13/SCK, R2.Pin_0, S3.1
  N11: Part1.D2, LED1.A
  N12: Part1.D3_PWM, LED1.B
  N13: Part1.D4, LED1.C
  N14: Part1.D5_PWM, LED1.D
  N15: Part1.D6_PWM, LED1.E
  N16: Part1.D7, LED1.F
  N17: Part1.5V, S2.3, S3.3
  N18: Part1.GND, R1.Pin_1, R2.Pin_1, LED2.cathode, J1.pin1
  N19: LED2.anode, R3.Pin_0
