# Fritzing sketch id822_Fritzing_Robo_Connections_0 (saved by Fritzing 0.7.12b)
breadboards: 1

parts:
  Arduino1 = Arduino
  J1 = Basic Servo
  J2 = Basic Servo
  VCC1 = Battery block 9V

nets:
  N1: Arduino1.D9, J1.pulse
  N2: Arduino1.D6, J2.pulse
  VCC: Arduino1.+5V, J1.vcc, J2.vcc
  GND: Arduino1.GND, J1.gnd, J2.gnd, VCC1.-
  N3: Arduino1.VIN, VCC1.+
