# Fritzing sketch id823_miniskybot2_hi_viz_0 (saved by Fritzing 0.8.7b)
circuit board: 9.52385cm x 5.84597cm
breadboards: 1

parts:
  Part1 = Arduino Uno (Rev3)
  BATT1 = 4xAA_Switchable_Battery_Pack_w_Bare_Wire
  J1 = Basic Servo
  J2 = Basic Servo
  PING)))_SENSOR1 = RL
  C1 = Electrolytic Capacitor [capacitance=1000μF package="1010 [SMD, electrolytic]"]
  J3 = Piezo Speaker
  LED1 = LED - 5mm [color="Red (633nm)" package="5 mm [THT]"]
  R1 = Resistor [tolerance=±5% resistance=220 package=THT]

nets (from the pcb view):
  N1: Part1.D9_PWM, J2.pulse
  N2: Part1.D10_PWM/SS, J1.pulse
  N3: Part1.D13/SCK, R1.Pin_1
  GND: Part1.GND, BATT1.connector2, J1.gnd, J2.gnd, PING)))_SENSOR1.connector8, C1.-, J3.pin1, LED1.cathode
  VCC: Part1.D2, Part1.VIN, BATT1.connector1, J1.vcc, J2.vcc, PING)))_SENSOR1.connector9, C1.+
  N4: Part1.D4, J3.pin2
  N5: LED1.anode, R1.Pin_0
