# Fritzing sketch id825_DHT22_arduino_lcd_sd_biTl90l_0 (saved by Fritzing 0.9.3b)
breadboards: 1

parts:
  Componente1 = Arduino Micro (Rev3)
  LCD1 = LCD screen
  R1 = Rotary Potentiometer (Small) [maximum_resistance=100kΩ package=THT]
  RHT1 = Humidity and Temperature Sensor RHT03
  R2 = Resistor [tolerance=±5% resistance=220 package=THT]
  U2 = microSD Socket [package="Molex 502774-0891 [SMD]"]

nets:
  GND: Componente1.GND, LCD1.VSS, LCD1.R/W, LCD1.LED-, R1.leg2, RHT1.Data-signal, RHT1.GND_2, U2.GND
  5V: Componente1.5V, LCD1.VDD, R1.leg1, RHT1.Vcc, R2.Pin_1
  N1: LCD1.V0, R1.wiper

notes:
  3.3 V
