# Fritzing sketch id828_sketchFritzing_AlarmaBasico_0 (saved by Fritzing 0.8.7b)
circuit board: 8.46667cm x 5.64444cm
breadboards: 1

parts:
  LED1 = LED - 5mm [color="Green (555nm)" package="5 mm [THT]"]
  LED2 = LED - 5mm [color="Red (633nm)" package="5 mm [THT]"]
  LED3 = LED - 5mm [color="White (8000K)" package="5 mm [THT]"]
  R1 = Resistor [tolerance=±5% resistance=220 package=THT]
  R2 = Resistor [tolerance=±5% resistance=220 package=THT]
  R3 = Resistor [tolerance=±5% resistance=220 package=THT]
  Parte1 = Arduino Uno (Rev3)
  S1 = Pushbutton [package=THT]
  R4 = Resistor [tolerance=±5% resistance=220 package=THT]
  J1 = Piezo Speaker
  U1 = RELAY [package=relay-jzc]
  R6 = Resistor [tolerance=±5% resistance=10k package=THT]

nets:
  N1: LED1.anode, R3.Pin_1
  N2: LED2.anode, R2.Pin_1
  N3: LED3.anode, R1.Pin_1
  N4: R1.Pin_0, U1.NC
  N5: R2.Pin_0, Parte1.D12/MISO
  N6: R3.Pin_0, Parte1.D13/SCK
  N7: Parte1.A0, R6.Pin_0
  N8: Parte1.D10_PWM/SS, J1.pin2
  N9: Parte1.D11_PWM/MOSI, U1.COIL2
  N10: Parte1.D3_PWM, S1.leg1
  N11: Parte1.5V, R4.Pin_0, J1.pin1, U1.MAIN
  N12: Parte1.GND, U1.NO, U1.COIL1, R6.Pin_1
  N13: S1.leg0, R4.Pin_1

notes:
  [Se ha utilizado un arduino yun]
