# Fritzing sketch id829_BasicPong_0 (saved by Fritzing 0.9.3b)
breadboards: 1

parts:
  Part1 = Arduino Uno (Rev3)
  S1 = Pushbutton [package="[THT]"]
  S2 = Pushbutton [package="[THT]"]
  R1 = Resistor [tolerance=±5% resistance=220 package=THT]
  R2 = Resistor [tolerance=±5% resistance=220 package=THT]
  R3 = Resistor [tolerance=±5% resistance=220 package=THT]
  R4 = Resistor [tolerance=±5% resistance=220 package=THT]
  R5 = Resistor [tolerance=±5% resistance=220 package=THT]
  R6 = Resistor [tolerance=±5% resistance=220 package=THT]
  LED1 = LED - 5mm [color="Red (633nm)" package="5 mm [THT]"]
  LED2 = LED - 5mm [color="Red (633nm)" package="5 mm [THT]"]
  LED3 = LED - 5mm [color="Red (633nm)" package="5 mm [THT]"]
  LED4 = LED - 5mm [color="Red (633nm)" package="5 mm [THT]"]
  LED5 = LED - 5mm [color="Red (633nm)" package="5 mm [THT]"]
  LED6 = LED - 5mm [color="Red (633nm)" package="5 mm [THT]"]
  R7 = Resistor [tolerance=±5% resistance=10k package=THT]
  R8 = Resistor [tolerance=±5% resistance=10k package=THT]

nets:
  N1: Part1.D11_PWM/MOSI, S2.Pin_3, S2.Pin_4, R8.Pin_0
  N2: Part1.D12/MISO, S1.Pin_1, S1.Pin_2, R7.Pin_0
  N3: Part1.GND, LED1.cathode, LED2.cathode, LED3.cathode, LED4.cathode, LED5.cathode, LED6.cathode, R7.Pin_1, R8.Pin_1
  N4: Part1.D2, R6.Pin_1
  N5: Part1.D3_PWM, R5.Pin_1
  N6: Part1.D4, R4.Pin_1
  N7: Part1.D5_PWM, R3.Pin_1
  N8: Part1.D6_PWM, R2.Pin_1
  N9: Part1.D7, R1.Pin_1
  N10: Part1.5V, S1.Pin_3, S1.Pin_4, S2.Pin_1, S2.Pin_2
  N11: R1.Pin_0, LED6.anode
  N12: R2.Pin_0, LED5.anode
  N13: R3.Pin_0, LED4.anode
  N14: R4.Pin_0, LED3.anode
  N15: R5.Pin_0, LED2.anode
  N16: R6.Pin_0, LED1.anode
