# Fritzing sketch id82_Arduino_2560_Black_Box_Sketch_002_0 (saved by Fritzing 0.9.3b)
breadboards: 1

parts:
  LCD1 = LCD screen
  2560 = Arduino Mega 2560 (Rev3)
  RTC = Real Time Clock Module - DS1307 RTC Breakout Board
  Piezo_Speaker = Piezo Speaker
  Keypad = Header 8 [package=1x08_smd_alt]
  R1 = Trimmer Potentiometer [maximum_resistance=10kΩ package=THT]

nets:
  GND: LCD1.VSS, LCD1.R/W, LCD1.LED-, 2560.GND, RTC.GND, Piezo_Speaker.pin2, R1.leg1
  5V: LCD1.VDD, LCD1.LED+, RTC.5V, R1.leg2
  N1: LCD1.V0, R1.wiper
  N2: LCD1.RS, 2560.D22
  N3: LCD1.E, 2560.D24
  N4: LCD1.DB4, 2560.D26
  N5: LCD1.DB5, 2560.D28
  N6: LCD1.DB6, 2560.D30
  N7: LCD1.DB7, 2560.D32
  N8: 2560.D21/SCL, 2560.SCL, RTC.SCL
  N9: 2560.D20/SDA, 2560.SDA, RTC.SDA
  N10: 2560.D37, Piezo_Speaker.pin1
  N11: 2560.D38, Keypad.8
  N12: 2560.D40, Keypad.7
  N13: 2560.D42, Keypad.6
  N14: 2560.D44, Keypad.5
  N15: 2560.D46, Keypad.4
  N16: 2560.D48, Keypad.3
  N17: 2560.D50, Keypad.2
  N18: 2560.D52, Keypad.1
