# Fritzing sketch id830_Basketball_Scoreboard_Arduino_parte_2_0 (saved by Fritzing 0.9.3b)
breadboards: 1

parts:
  Componente1 = Arduino Nano (Rev3.0)
  Matrix_keypad1 = CMG
  LCM1602_IIC2 = generic_ic_dip_22_300mil.fzp [part_number="LCM1602 IIC" chip_label="LCM1602 IIC"]
  J1 = Power Jack [package=power_jack_pth_lock]  # not connected

nets:
  N1: Componente1.GND, LCM1602_IIC2.connector16
  N2: Componente1.D3, Matrix_keypad1.connector25
  N3: Componente1.D4, Matrix_keypad1.connector26
  N4: Componente1.D5, Matrix_keypad1.connector27
  N5: Componente1.D6, Matrix_keypad1.connector28
  N6: Componente1.D8, Matrix_keypad1.connector29
  N7: Componente1.D9, Matrix_keypad1.connector30
  N8: Componente1.D10, Matrix_keypad1.connector31
  N9: Componente1.D11/MOSI, Matrix_keypad1.connector32
  N10: Componente1.A5, LCM1602_IIC2.connector19
  N11: Componente1.A4, LCM1602_IIC2.connector18

notes:
  Conector Fonte 5V
  Interface PCF8574
