# Fritzing sketch id831_Arduino_Auto_Sprayer_Schematic_0 (saved by Fritzing 0.9.3b)
breadboards: 1

parts:
  VCC1 = Battery
  Part1 = Arduino Nano (Rev3.0)
  R1 = Resistor [tolerance=±5% resistance=220 package=THT]
  Q1 = NPN-Transistor [package="TO92 [THT]"]
  D1 = Rectifier Diode [part_number=1N4001 package="300 mil [THT]"]
  M1 = DC Motor

nets:
  N1: VCC1.-, Part1.D2, Q1.E
  N2: VCC1.+, D1.anode
  N3: Part1.GND, R1.Pin_0
  N4: R1.Pin_1, Q1.C
  N5: Q1.B, D1.cathode, M1.pin_1

notes:
  DC Motor (squirt motor)
