# Fritzing sketch id833_medidor_bateria_0 (saved by Fritzing 0.3.15b)
breadboards: 1

parts:
  Arduino1 = Arduino
  LED1 = green LED - 5mm
  LED2 = yellow LED - 5mm
  LED3 = Red LED - 5mm
  R1 = Resistor [resistance=1k package=THT]
  R2 = Resistor [resistance=1k package=THT]
  R3 = Resistor [resistance=1k package=THT]
  R4 = Resistor [resistance=10k package=THT]
  R5 = Resistor [resistance=10k package=THT]
  VCC1 = obsolete Battery

nets:
  N1: Arduino1.GND, LED1.cathode, LED2.cathode, LED3.cathode
  N2: Arduino1.D12, R1.Pin_1
  N3: Arduino1.D11, R2.Pin_1
  N4: Arduino1.D10, R3.Pin_1
  N5: Arduino1.A0, R4.Pin_1, R5.Pin_0
  N6: LED1.anode, R1.Pin_0
  N7: LED2.anode, R2.Pin_0
  N8: LED3.anode, R3.Pin_0
  N9: R4.Pin_0, VCC1.-
  N10: R5.Pin_1, VCC1.+
