# Fritzing sketch id834_BatteryMonitor_0 (saved by Fritzing 0.9.2b)
circuit board: 2.40445cm x 8.98529cm
breadboards: 1

parts:
  Arduino_Pro_Mini = Arduino Pro Mini v13
  Q1 = Basic FET N-Channel [package="TO220 [THT]"]
  R1 = Resistor [tolerance=±5% resistance=2.2k package=THT]
  R2 = Resistor [tolerance=±5% resistance=2.2k package=THT]
  R3 = Resistor [tolerance=±5% resistance=3.3 package=THT]
  T1 = LM35 Temperature Sensor [package="TO92 [THT]"]
  C1 = Electrolytic Capacitor [capacitance=1µF voltage=16V package="0605 [SMD, electrolytic]"]
  OUT = screw terminal, 2 pins
  BATTERY = screw terminal, 2 pins
  8A = FUSE [package=fuse_5mm]
  Ping = smd LED [color="Blue (525nm)" package="0805 [SMD]"]

nets:
  N1: Arduino_Pro_Mini.RAW, R2.Pin_0, T1.+Vs, C1.+, OUT.pin2, BATTERY.pin1
  GND: Arduino_Pro_Mini.GND, Q1.source, T1.GND, C1.-, 8A.1, Ping.cathode
  N2: Arduino_Pro_Mini.A2, T1.Vout
  N3: Arduino_Pro_Mini.A0, R2.Pin_1, R3.Pin_0
  N4: Arduino_Pro_Mini.D8, Ping.anode
  N5: Arduino_Pro_Mini.D2, R1.Pin_0
  N6: Q1.gate, R1.Pin_1
  N7: Q1.drain, R3.Pin_1, OUT.pin1
  N8: BATTERY.pin2, 8A.2

notes:
  +
  -
  BattMon r1
  2017 Alex v.
