# Fritzing sketch id835_Untitled_Sketch_0 (saved by Fritzing 0.9.3b)
breadboards: 1

parts:
  Componente1 = Arduino Uno (Rev3)
  M1 = DC Motor
  M2 = DC Motor
  Componente4 = Bluetooth Mate Silver
  IC1 = H-Bridge [package=THT]
  Componente6 = Tri-Axis Gyro Breakout - L3G4200D
  VCC1 = Battery block 9V

nets (from the breadboard view):
  N1: Componente1.A4/SDA, Componente6.SDA
  N2: Componente1.A5/SCL, Componente6.SCL
  GND: Componente1.GND, Componente4.TX_5V, IC1.GND1, IC1.GND2, Componente6.GND, VCC1.-
  N3: Componente1.D6_PWM, IC1.2A
  N4: Componente1.D7, IC1.1A
  3V3: Componente1.3V3, Componente6.VCC, Componente6.CS
  N5: Componente1.VIN, IC1.1_2EN, IC1.VCC2, IC1.VCC1, VCC1.+
  N6: M1.pin_1, IC1.4Y
  N7: M1.pin_2, IC1.3Y
  N8: M2.pin_1, IC1.1Y
  N9: M2.pin_2, IC1.2Y
  GND3: IC1.GND3, IC1.GND4
