# Fritzing sketch id836_Bryan_Smith_0 (saved by Fritzing 0.9.3b)
breadboards: 1

parts:
  Raspberry_Pi_1 = Raspberry Pi 3 [part_number=RPI-3-V1.2]  # not connected
  M1 = DC Motor  # not connected
  M2 = DC Motor  # not connected
  M3 = DC Motor  # not connected
  M4 = DC Motor  # not connected
  IC1 = H-Bridge [package=THT]  # not connected
  IC2 = H-Bridge [package=THT]  # not connected
  IC3 = H-Bridge [package=THT]  # not connected
  IC4 = H-Bridge [package=THT]  # not connected
  hc-sr1 = hc-sr04  # not connected
  hc-sr2 = hc-sr04  # not connected
  hc-sr3 = hc-sr04  # not connected
  hc-sr4 = hc-sr04  # not connected
  LED1 = LEDs [package=led10mm]  # not connected
  LED3 = LEDs [package=led10mm]  # not connected
  LED4 = LEDs [package=led10mm]  # not connected
  LED5 = LEDs [package=led10mm]  # not connected
  U1 = LIPO-2000mAh [package=lipo-2000]
  Part2 = PowerBoost 500 Charger

nets:
  N1: U1.+, Part2.VBAT_IN
  N2: U1.-, Part2.GND_BAT_IN
