# Fritzing sketch id837_bbqtherm_0 (saved by Fritzing 0.9.3b)
breadboards: 1

parts:
  Part1 = Spark Core (v1.0)
  R1 = Resistor [tolerance=±1% resistance=10 package=THT]
  U1 = 2.5mm Audio Jack [package=stereojack2.5mm_stereojack2.5mm]  # not connected

nets:
  N1: Part1.GND, R1.Pin_0
