# Fritzing sketch id838_Lab2_RCTime_LED_0 (saved by Fritzing 0.8.7b)
breadboards: 1

parts:
  Part1 = Arduino Uno (Rev3)
  R1 = Resistor [tolerance=±5% resistance=220 package="0805 [SMD]"]
  LED1 = LED - 5mm [color="Red (633nm)" package="5 mm [THT]"]
  C2 = Capacitor [package=cap-pth-small2]

nets:
  N1: Part1.A1, R1.Pin_0
  N2: Part1.5V, C2.1
  N3: Part1.GND, LED1.anode
  N4: R1.Pin_1, LED1.cathode, C2.2
