# Fritzing sketch id841_EM406_0 (saved by Fritzing 0.9.3b)
circuit board: 12cm x 10cm
breadboards: 1

parts:
  U1 = EM406 GPS Connector [package=em406]
  R1 = Rotary Potentiometer (Small) [maximum_resistance=100kΩ package=THT]
  R2 = Resistor [tolerance=±5% resistance=220 package=THT]
  LCD1 = LCD screen
  Componente1 = Arduino Mega 2560 (Rev3)

nets:
  VCC: U1.VCC, R1.leg2, R2.Pin_1, LCD1.VDD
  N1: U1.RX, Componente1.D18/TX1
  N2: U1.TX, Componente1.D19/RX1
  GND2: U1.GND2, R1.leg1, LCD1.VSS, LCD1.R/W, LCD1.LED-
  N3: R1.wiper, LCD1.V0
  N4: R2.Pin_0, LCD1.LED+
  N5: LCD1.RS, Componente1.D12_PWM
  N6: LCD1.E, Componente1.D11_PWM
  N7: LCD1.DB4, Componente1.D5_PWM
  N8: LCD1.DB5, Componente1.D4_PWM
  N9: LCD1.DB6, Componente1.D3_PWM
  N10: LCD1.DB7, Componente1.D2_PWM
