# Fritzing sketch id842_Audio_Volume_Stereo (saved by Fritzing 0.5.2b)
breadboards: 1

parts:
  R1 = Rotary Potentiometer (Large) [package=THT]
  Output = Stereo Jack (TRS) 3.5mm [package="PG203J [THT]"]
  Input = Stereo Jack (TRS) 3.5mm [package="PG203J [THT]"]
  R1_2 = Rotary Potentiometer (Large) [package=THT]

nets:
  N1: R1.wiper, Output.Ring, Output.Tip, R1_2.wiper
  N2: R1.leg2, Input.Ring, Input.Tip, R1_2.leg2
  N3: Output.Sleeve, Input.Sleeve

notes:
  No connection on the bottom leg of the pots
  This is the stero version.
  You can buy stereo pots, they are more expensive. They only have one knob so its not confusing to the end user
