# Fritzing sketch id842_CMPS11_0 (saved by Fritzing 0.9.3b)
circuit board: 8.46667cm x 10cm
breadboards: 1

parts:
  LCD1 = LCD screen  # not connected
  Componente1 = Arduino Mega 2560 (Rev3)
  J2 = single row smd male pin header, 4 pins [form="♂ (male)"]
  R1 = Resistor [tolerance=±5% resistance=2.2k package=THT]
  R2 = Resistor [tolerance=±5% resistance=2.2k package=THT]
  J3 = male pin header, 6 pins [form="♂ (male)"]
  Componente2 = adafruit [part_number="Adafruit #746"]
  J4 = Basic Servo

nets:
  N1: Componente1.D21/SCL, J2.pin2, R2.Pin_1, J3.pin4
  N2: Componente1.D20/SDA, J2.pin3, R1.Pin_1, J3.pin5
  N3: Componente1.D19/RX1, Componente2.connector16
  N4: Componente1.D18/TX1, Componente2.connector15
  GND: Componente1.GND, J2.pin1, J3.pin1, Componente2.connector14, J4.gnd
  N5: Componente1.D11_PWM, J4.pulse
  5V: Componente1.5V, J2.pin4, R1.Pin_0, R2.Pin_0, J3.pin6, Componente2.connector13, J4.vcc

notes:
  [Robot Electronics 20x4 LCD05
  I2C/Serial LCD
  I2C mode
  connections on the backplane:
  Vcc(5V)
  SDA/TX
  SCL/RX
  GND
  Jumper open
  CMPS11 Compass
  I2C mode
  PINS:
  Vcc(3.6/5V)
  SDA
  SCL
  MODE PIN
  FACTORY USE
  GROUND
  CMPS11 Pins
  LCD I2C Pins
