# Fritzing sketch id843_Auduino_Theramin (saved by Fritzing 0.3.15b)
breadboards: 1

parts:
  R1 = Trimmer Potentiometer [package=THT]
  R2 = Trimmer Potentiometer [package=THT]
  R3 = Trimmer Potentiometer [package=THT]
  R4 = Trimmer Potentiometer [package=THT]
  R5 = Trimmer Potentiometer [package=THT]
  Arduino1 = Arduino
  R6 = Photocell (LDR) [package=THT]
  S3 = Toggle Switch [package=THT]
  R7 = Resistor [resistance=10 package=THT]
  S4 = Toggle Switch [package=THT]
  SPKR1 = Loudspeaker

nets:
  N1: R1.leg1, R2.leg1, R3.leg1, R4.leg1, R5.leg1, Arduino1.+5V, S4.L1
  N2: R1.wiper, Arduino1.A0
  N3: R1.leg2, R2.leg2, R3.leg2, R4.leg2, R5.leg2, Arduino1.GND, S4.L2, SPKR1.pin1
  N4: R2.wiper, Arduino1.A2
  N5: R3.wiper, Arduino1.A3
  N6: R4.wiper, S3.L1
  N7: R5.wiper, Arduino1.A1
  N8: Arduino1.D5, S4.COM
  N9: Arduino1.D3, SPKR1.pin2
  N10: Arduino1.A4, S3.COM
  N11: R6.pin_0, S3.L2, R7.Pin_0, R7.Pin_1

notes:
  SWITCH: Smooth Frequency Mappin-g vs. Pentatonic
  SWITCH: Potentiometer and LDR
  Audio Jack
