# Fritzing sketch id843_BeeCounter_0 (saved by Fritzing 0.9.2b)
circuit board: 6.66716cm x 10.1903cm
breadboards: 1

parts:
  LDR = Photocell (LDR) [part_number=12 package=THT]
  R2 = Resistor [tolerance=±5% resistance=220 package=THT]
  LDR1 = Photocell (LDR) [part_number=12 package=THT]
  R3 = Resistor [tolerance=±5% resistance=220 package=THT]
  R4 = Resistor [tolerance=±5% resistance=220 package=THT]
  R5 = Resistor [tolerance=±5% resistance=220 package=THT]
  R6 = Resistor [tolerance=±5% resistance=220 package=THT]
  R7 = Resistor [tolerance=±5% resistance=220 package=THT]
  LDR2 = Photocell (LDR) [part_number=12 package=THT]
  LDR3 = Photocell (LDR) [part_number=12 package=THT]
  LDR4 = Photocell (LDR) [part_number=12 package=THT]
  LDR5 = Photocell (LDR) [part_number=12 package=THT]
  R8 = Resistor [tolerance=±5% resistance=220 package=THT]
  R9 = Resistor [tolerance=±5% resistance=220 package=THT]
  R10 = Resistor [tolerance=±5% resistance=220 package=THT]
  R11 = Resistor [tolerance=±5% resistance=220 package=THT]
  R12 = Resistor [tolerance=±5% resistance=220 package=THT]
  R13 = Resistor [tolerance=±5% resistance=220 package=THT]
  LDR6 = Photocell (LDR) [part_number=12 package=THT]
  LDR7 = Photocell (LDR) [part_number=12 package=THT]
  LDR8 = Photocell (LDR) [part_number=12 package=THT]
  LDR9 = Photocell (LDR) [part_number=12 package=THT]
  LDR10 = Photocell (LDR) [part_number=12 package=THT]
  LDR11 = Photocell (LDR) [part_number=12 package=THT]
  R14 = Resistor [tolerance=±5% resistance=220 package=THT]
  LDR2_2 = Photocell (LDR) [part_number=12 package=THT]
  R3_2 = Resistor [tolerance=±5% resistance=220 package=THT]
  LDR3_2 = Photocell (LDR) [part_number=12 package=THT]
  R0 = Resistor [tolerance=±5% resistance=220 package=THT]
  LDR0 = Photocell (LDR) [part_number=12 package=THT]
  R1 = Resistor [tolerance=±5% resistance=220 package=THT]
  LDR1_2 = Photocell (LDR) [part_number=12 package=THT]
  Multiplexer_CD74HC4067 = Analog Digital MUX Breakout

nets:
  N1: LDR.pin_0, R2.Pin_1, Multiplexer_CD74HC4067.C4
  N2: LDR.pin_1, LDR1.pin_0, LDR2.pin_1, LDR3.pin_0, LDR4.pin_1, LDR5.pin_0, LDR6.pin_0, LDR7.pin_1, LDR8.pin_1, LDR9.pin_1, LDR10.pin_0, LDR11.pin_0, LDR2_2.pin_0, LDR3_2.pin_1, LDR0.pin_0, LDR1_2.pin_1, Multiplexer_CD74HC4067.VCC
  N3: R2.Pin_0, R3.Pin_1, R4.Pin_1, R5.Pin_0, R6.Pin_0, R7.Pin_1, R8.Pin_1, R9.Pin_0, R10.Pin_1, R11.Pin_0, R12.Pin_0, R13.Pin_1, R14.Pin_1, R3_2.Pin_0, R0.Pin_1, R1.Pin_0, Multiplexer_CD74HC4067.GND
  N4: LDR1.pin_1, R3.Pin_0, Multiplexer_CD74HC4067.C5
  N5: R4.Pin_0, LDR3.pin_1, Multiplexer_CD74HC4067.C7
  N6: R5.Pin_1, LDR2.pin_0, Multiplexer_CD74HC4067.C6
  N7: R6.Pin_1, LDR4.pin_0, Multiplexer_CD74HC4067.C8
  N8: R7.Pin_0, LDR5.pin_1, Multiplexer_CD74HC4067.C9
  N9: R8.Pin_0, LDR11.pin_1, Multiplexer_CD74HC4067.C11
  N10: R9.Pin_1, LDR9.pin_0, Multiplexer_CD74HC4067.C10
  N11: R10.Pin_0, LDR10.pin_1, Multiplexer_CD74HC4067.C13
  N12: R11.Pin_1, LDR8.pin_0, Multiplexer_CD74HC4067.C12
  N13: R12.Pin_1, LDR7.pin_0, Multiplexer_CD74HC4067.C14
  N14: R13.Pin_0, LDR6.pin_1, Multiplexer_CD74HC4067.C15
  N15: R14.Pin_0, LDR2_2.pin_1, Multiplexer_CD74HC4067.C3
  N16: R3_2.Pin_1, LDR3_2.pin_0, Multiplexer_CD74HC4067.C2
  N17: R0.Pin_0, LDR0.pin_1, Multiplexer_CD74HC4067.C1
  N18: R1.Pin_1, LDR1_2.pin_0, Multiplexer_CD74HC4067.C0
