# Fritzing sketch id845_Force_Resistor_triggered_piezo_0 (saved by Fritzing 0.8.3b)
breadboards: 1

parts:
  J1 = Piezo Speaker
  C1 = Ceramic Capacitor [capacitance=100nF package="100 mil [THT, multilayer]"]
  U2 = 555 Timer [package="DIP8 [THT]"]
  U3 = LM 358 Dual Op-Amp [package="DIP8 [THT]"]
  R1 = Resistor [tolerance=±5% resistance=22k package=THT]
  C2 = Ceramic Capacitor [capacitance=100nF package="100 mil [THT, multilayer]"]
  R4 = Resistor [tolerance=±5% resistance=10k package=THT]
  R3 = Resistor [tolerance=±5% resistance=10k package=THT]
  C3 = Ceramic Capacitor [capacitance=10nF package="100 mil [THT, multilayer]"]
  R2 = Trimmer Potentiometer [package=THT]
  J2 = Basic Force Sensing Resistor (FSR) [package=THT]

nets:
  GND: J1.pin1, U2.Ground, U3.connector3, R1.Pin_1, C3.0, R2.leg1
  N1: J1.pin2, C1.1
  N2: C1.0, U2.Output
  N3: U2.Trigger, U2.Threshold, R4.Pin_0, C3.1
  N4: U2.Reset, U3.connector0
  N5: U2.Control_Voltage, C2.1
  N6: U2.Discharge, R4.Pin_1, R3.Pin_1
  5V: U2.Vcc_Supply_Voltage, U3.connector7, C2.0, R3.Pin_0, R2.leg2, J2.pin_0
  N7: U3.connector1, R2.wiper
  N8: U3.connector2, R1.Pin_0, J2.pin_1

notes:
  555 timer creates a 50% duty cycle square wave at roughly 4.4kHz for the piezo
  You can put a resistor between output and - on the op-amp to reduce noise, but I found it made things more finiky (i.e. could create feedback loop and pin the output high or low)
