# Fritzing sketch id846_Buttons_and_LEDs_X2_0 (saved by Fritzing 0.9.3b)
breadboards: 1

parts:
  R2 = Resistor [tolerance=±5% resistance=220 package=THT]
  LED1 = LED - 5mm [color="Red (633nm)" package="5 mm [THT]"]
  LED2 = LED - 5mm [color="Yellow (595nm)" package="5 mm [THT]"]
  S1 = Pushbutton [package="[THT]"]  # not connected
  S2 = Pushbutton [package="[THT]"]
  Part1 = Arduino Uno (Rev3)
  R5 = Resistor [tolerance=±5% resistance=220 package=THT]
  R6 = Resistor [tolerance=±5% resistance=220 package=THT]
  R7 = Resistor [tolerance=±5% resistance=220 package=THT]
  Power_plug1 = Power plug  # not connected

nets:
  N1: R2.Pin_0, Part1.D9_PWM
  N2: R2.Pin_1, Part1.GND, R5.Pin_1, R6.Pin_1, R7.Pin_1
  N3: LED1.cathode, R7.Pin_0
  N4: LED1.anode, Part1.D8
  N5: LED2.cathode, R6.Pin_0
  N6: LED2.anode, Part1.D10_PWM/SS
  N7: S2.Pin_1, S2.Pin_2, Part1.D6_PWM, R5.Pin_0
  N8: S2.Pin_3, S2.Pin_4, Part1.5V
