# Fritzing sketch id847_Belote_0 (saved by Fritzing 0.9.2b)
breadboards: 3

parts:
  Part1 = Arduino Mega ADK (Rev3)
  7_Segment3 = 7 Segment Display
  7_Segment4 = 7 Segment Display
  7_Segment5 = 7 Segment Display
  7_Segment6 = 7 Segment Display
  7_Segment8 = 7 Segment Display
  7_Segment7 = 7 Segment Display
  S14 = Pushbutton [package="[THT]"]
  S15 = Pushbutton [package="[THT]"]
  S16 = Pushbutton [package="[THT]"]
  S17 = Pushbutton [package="[THT]"]
  S18 = Pushbutton [package="[THT]"]
  S19 = Pushbutton [package="[THT]"]
  S20 = Pushbutton [package="[THT]"]
  S21 = Pushbutton [package="[THT]"]
  S22 = Pushbutton [package="[THT]"]
  S23 = Pushbutton [package="[THT]"]
  S24 = Pushbutton [package="[THT]"]
  S25 = Pushbutton [package="[THT]"]

nets:
  N1: Part1.A0, S14.Pin_3, S14.Pin_4, S17.Pin_3, S17.Pin_4, S18.Pin_3, S18.Pin_4
  N2: Part1.A1, S15.Pin_3, S15.Pin_4, S16.Pin_3, S16.Pin_4, S19.Pin_3, S19.Pin_4
  N3: Part1.A2, S22.Pin_3, S22.Pin_4, S23.Pin_3, S23.Pin_4, S24.Pin_3, S24.Pin_4
  N4: Part1.A3, S20.Pin_3, S20.Pin_4, S21.Pin_3, S21.Pin_4, S25.Pin_3, S25.Pin_4
  N5: Part1.D21/SCL, S14.Pin_1, S14.Pin_2, S15.Pin_1, S15.Pin_2, S21.Pin_1, S21.Pin_2, S22.Pin_1, S22.Pin_2
  N6: Part1.D20/SDA, S17.Pin_1, S17.Pin_2, S19.Pin_1, S19.Pin_2, S20.Pin_1, S20.Pin_2, S24.Pin_1, S24.Pin_2
  N7: Part1.D19/RX1, S16.Pin_1, S16.Pin_2, S18.Pin_1, S18.Pin_2, S23.Pin_1, S23.Pin_2, S25.Pin_1, S25.Pin_2
  N8: Part1.D31, 7_Segment3.Segment_A#10, 7_Segment4.Segment_A#10, 7_Segment5.Segment_A#10, 7_Segment6.Segment_A#10, 7_Segment8.Segment_A#10, 7_Segment7.Segment_A#10
  N9: Part1.D32, 7_Segment3.Segment_B, 7_Segment4.Segment_B, 7_Segment5.Segment_B, 7_Segment6.Segment_B, 7_Segment8.Segment_B, 7_Segment7.Segment_B
  N10: Part1.D33, 7_Segment3.Segment_C, 7_Segment4.Segment_C, 7_Segment4.common_cathode#8, 7_Segment5.Segment_C, 7_Segment5.common_cathode#8, 7_Segment6.Segment_C, 7_Segment8.Segment_C, 7_Segment8.common_cathode#8, 7_Segment7.Segment_C, 7_Segment7.common_cathode#8
  N11: Part1.D34, 7_Segment3.Segment_D, 7_Segment4.Segment_D, 7_Segment5.Segment_D, 7_Segment6.Segment_D, 7_Segment8.Segment_D, 7_Segment7.Segment_D
  N12: Part1.D35, Part1.D41, Part1.D43, Part1.D44, Part1.D46, 7_Segment3.Segment_E, 7_Segment4.common_cathode#3, 7_Segment4.Segment_E, 7_Segment5.common_cathode#3, 7_Segment5.Segment_E, 7_Segment6.Segment_E, 7_Segment8.common_cathode#3, 7_Segment8.Segment_E, 7_Segment7.common_cathode#3, 7_Segment7.Segment_E
  N13: Part1.D36, 7_Segment3.Segment_F, 7_Segment4.Segment_F, 7_Segment5.Segment_F, 7_Segment6.Segment_F, 7_Segment8.Segment_F, 7_Segment7.Segment_F
  N14: Part1.D37, 7_Segment3.Segment_A#1, 7_Segment4.Segment_A#1, 7_Segment5.Segment_A#1, 7_Segment6.Segment_A#1, 7_Segment8.Segment_A#1, 7_Segment7.Segment_A#1
  N15: Part1.D42, 7_Segment3.common_cathode
  N16: Part1.D45, 7_Segment6.common_cathode
