# Fritzing sketch id848_BEND_SENSOR_0 (saved by Fritzing 0.9.2b)
stripboards: 1

parts:
  Part1 = Arduino Uno (Rev3)
  R1 = Resistor [tolerance=±5% resistance=18 package=THT]
  J1 = Piezo Speaker
  GY2 = MPU-6050 GY-521 [form="♀ (female)"]
  Part2 = Bluetooth HC-05 Macho
  R2 = Basic Flex Resistor

nets:
  N1: Part1.A0, R1.Pin_1, R2.pin_1
  N2: Part1.A4/SDA, GY2.connector3
  N3: Part1.A5/SCL, GY2.connector2
  N4: Part1.D9_PWM, J1.pin2
  GND: Part1.GND, J1.pin1, GY2.connector1, Part2.GND, R2.Pin_2
  N5: Part1.D0/RX, Part2.RXD
  N6: Part1.D1/TX, Part2.TXD
  N7: Part1.D2, GY2.connector7
  3V3: Part1.3V3, Part2.VCC
  N8: Part1.5V, R1.Pin_0, GY2.connector0
