# Fritzing sketch id849_finalsketch2_0 (saved by Fritzing 0.9.3b)
breadboards: 1

parts:
  Part1 = Arduino Pro Mini v13
  R1 = Resistor [tolerance=±5% resistance=220 package=THT]
  R2 = Resistor [tolerance=±5% resistance=220 package=THT]
  R3 = Resistor [tolerance=±5% resistance=220 package=THT]
  R4 = Resistor [tolerance=±5% resistance=220 package=THT]
  VCC2 = Battery
  Q1 = NPN-Transistor [package="TO92 [THT]"]
  D1 = Diode [package=diode-1n4001]
  C1 = Capacitor [package=cap-pth-small]
  Q2 = NPN-Transistor [package="TO92 [THT]"]
  D2 = Diode [package=diode-1n4001]
  C2 = Capacitor [package=cap-pth-small]
  D3 = Diode [package=diode-1n4001]
  C3 = Capacitor [package=cap-pth-small]
  Q3 = NPN-Transistor [package="TO92 [THT]"]
  D4 = Diode [package=diode-1n4001]
  C4 = Capacitor [package=cap-pth-small]
  Q4 = NPN-Transistor [package="TO92 [THT]"]
  U3 = Vibration Motor- ROB-08449 [package=vibe-motor-10mm]
  U4 = Vibration Motor- ROB-08449 [package=vibe-motor-10mm]
  U5 = Vibration Motor- ROB-08449 [package=vibe-motor-10mm]
  U6 = Vibration Motor- ROB-08449 [package=vibe-motor-10mm]
  J5 = Infrared Proximity Sensor
  J7 = Infrared Proximity Sensor
  J6 = Infrared Proximity Sensor
  J4 = Infrared Proximity Sensor
  VCC3 = Battery

nets:
  N1: Part1.A3, J7.Vout
  N2: Part1.A2, J5.Vout
  N3: Part1.A1, J6.Vout
  N4: Part1.A0, J4.Vout
  N5: Part1.D9_PWM, R4.Pin_1
  N6: Part1.D6_PWM, R1.Pin_1
  N7: Part1.D5_PWM, R2.Pin_1
  N8: Part1.D3_PWM, R3.Pin_1
  N9: R1.Pin_0, Q3.B
  N10: R2.Pin_0, Q2.B
  N11: R3.Pin_0, Q1.B
  N12: R4.Pin_0, Q4.B
  N13: VCC2.-, Q1.E, Q2.E, Q3.E, Q4.E
  N14: VCC2.+, U3.+, U4.+, U6.+
  N15: Q1.C, C1.1
  N16: D1.C, C1.2, U3.-
  N17: Q2.C, C2.1
  N18: D2.C, C2.2, U4.-
  N19: D3.C, C3.2, U5.-
  N20: C3.1, Q3.C
  N21: D4.C, C4.2, U6.-
  N22: C4.1, Q4.C
  GND: J5.GND, J7.GND, J6.GND, J4.GND, VCC3.-
  VCC: J5.Vcc, J7.Vcc, J6.Vcc, J4.Vcc, VCC3.+
