# Fritzing sketch id84_2FotoResistencias2Leds2Motores_0 (saved by Fritzing 0.9.3b)
breadboards: 1

parts:
  R1 = Resistor [tolerance=±5% resistance=220 package=THT]
  R2 = Resistor [tolerance=±5% resistance=220 package=THT]
  R3 = Photocell (LDR) [package=THT]
  R4 = Photocell (LDR) [package=THT]
  R5 = Resistor [tolerance=±5% resistance=10k package=THT]
  R6 = Resistor [tolerance=±5% resistance=10k package=THT]
  BAT1 = BC9VPC [package=bc9vpc]
  Componente1 = Arduino Uno (Rev3)
  S1 = Ponte-H L298N
  M1 = DC Motor
  M2 = DC Motor
  LED1 = smd LED [color="Red (633nm)" package="0603 [SMD]"]
  LED2 = smd LED [color="Red (633nm)" package="0603 [SMD]"]

nets:
  N1: R1.Pin_0, LED2.cathode
  N2: R1.Pin_1, R2.Pin_0, R5.Pin_1, R6.Pin_1, Componente1.GND
  N3: R2.Pin_1, LED1.cathode
  N4: R3.pin_0, R4.pin_0, Componente1.5V
  N5: R3.pin_1, R5.Pin_0, Componente1.A1
  N6: R4.pin_1, R6.Pin_0, Componente1.A0
  N7: BAT1.V+, S1.connector1
  N8: BAT1.V-, S1.connector2
  N9: Componente1.D8, S1.connector8
  N10: Componente1.D9_PWM, S1.connector7
  N11: Componente1.D10_PWM/SS, S1.connector6
  N12: Componente1.D11_PWM/MOSI, S1.connector5
  N13: Componente1.D2, LED2.anode
  N14: Componente1.D3_PWM, LED1.anode
  N15: S1.connector10, M2.pin_2
  N16: S1.connector11, M2.pin_1
  N17: S1.connector13, M1.pin_2
  N18: S1.connector14, M1.pin_1
