# Fritzing sketch id851_PowerIndicator.00_0 (saved by Fritzing 0.9.2b)
circuit board: 3.64299cm x 2.41026cm
breadboards: 1

parts:
  U1 = LM 358 Dual Op-Amp [part_number="LM358 or TS393CN" package="DIP8 [THT]"]
  R1 = Resistor [tolerance=±5% resistance=25k package=THT]
  R2 = Resistor [tolerance=±5% resistance=1M package=THT]
  R3 = Resistor [tolerance=±5% resistance=50k package=THT]
  R4 = Resistor [tolerance=±5% resistance=39k package=THT]
  R5 = Resistor [tolerance=±5% resistance=50k package=THT]
  D1 = Zener Diode [part_number=BZX79-C3V9 breakdown_voltage=3.9V package="300 mil [THT]"]
  R6 = Resistor [tolerance=±5% resistance=10k package=THT]
  R7 = Resistor [tolerance=±5% resistance=10k package=THT]
  LED1 = DUO LED RG [part_number=SSL-LX3059IGW-CA package="5 mm [THT]"]
  8x_AA_or_3x_18605 = DC Power [voltage=12V]

nets:
  N1: U1.connector0, U1.connector5, R2.Pin_1, R6.Pin_0
  N2: U1.connector1, R3.Pin_0, R4.Pin_1
  N3: U1.connector2, R1.Pin_1, R2.Pin_0
  GND: U1.connector3, R4.Pin_0, D1.anode, 8x_AA_or_3x_18605.V-
  N4: U1.connector4, R1.Pin_0, R5.Pin_0, D1.cathode
  N5: U1.connector6, R7.Pin_0
  12V: U1.connector7, R3.Pin_1, R5.Pin_1, LED1.common_cathode, 8x_AA_or_3x_18605.V+
  N6: R6.Pin_1, LED1.green_anode
  N7: R7.Pin_1, LED1.red_anode

notes:
  Power Indicator, Power on and low battery indicator.  Glows green if battery voltage >8.9V.   Glows red otherwise., 0.2
