# Fritzing sketch id852_PowerIndicator.02_0 (saved by Fritzing 0.9.2b)
circuit board: 3.63028cm x 2.86795cm
breadboards: 1

parts:
  U1 = LM 358 Dual Op-Amp [part_number="LM358 or TS393CN" package="DIP8 [THT]"]
  R2 = Resistor [tolerance=±5% resistance=1.5M package=THT]
  R3 = Resistor [tolerance=±5% resistance=50k package=THT]
  R4 = Resistor [tolerance=±5% resistance=39k package=THT]
  R5 = Resistor [tolerance=±5% resistance=150 package=THT]
  R6 = Resistor [tolerance=±5% resistance=150 package=THT]
  8x_AA_or_3x_18605 = DC Power [voltage=12V]
  U2 = V_REG_LD1117VXX [part_number="3.3V Switching step-down, e.g. Pololu D24V5F3" package=78xxl]
  LED1 = DUO LED RG [part_number=SSL-LX3059IGW-CA package="5 mm [THT]"]
  R8 = Resistor [tolerance=±5% resistance=160k package=THT]
  R1 = Resistor [tolerance=±5% resistance=25k package=THT]
  R7 = Resistor [tolerance=±5% resistance=160k package=THT]

nets:
  N1: U1.connector0, U1.connector5, R2.Pin_1, R5.Pin_0
  N2: U1.connector1, R3.Pin_0, R4.Pin_1
  N3: U1.connector2, R2.Pin_0, R1.Pin_1
  GND: U1.connector3, R4.Pin_0, 8x_AA_or_3x_18605.V-, U2.GND, R8.Pin_0
  N4: U1.connector4, R8.Pin_1, R7.Pin_0
  N5: U1.connector6, R6.Pin_0
  N6: U1.connector7, R3.Pin_1, 8x_AA_or_3x_18605.V+, U2.IN
  N7: R5.Pin_1, LED1.green_anode
  N8: R6.Pin_1, LED1.red_anode
  N9: U2.OUT, LED1.common_cathode, R1.Pin_0, R7.Pin_1

notes:
  Power Indicator, Power on and low battery indicator.  Glows green if battery voltage >8.9V.  Red otherwise., 0.3
  With 3.3V switching step-down, total current consumed is kept under 5mA at all battery voltages.
