# Fritzing sketch id853_PowerIndicatorBlinker.02_0 (saved by Fritzing 0.9.2b)
breadboards: 1

parts:
  U1 = LM 358 Dual Op-Amp [part_number=TS393CN package="DIP8 [THT]"]
  R1 = Resistor [tolerance=±5% resistance=25k package=THT]
  R2 = Resistor [tolerance=±5% resistance=1M package=THT]
  R3 = Resistor [tolerance=±5% resistance=50k package=THT]
  R4 = Resistor [tolerance=±5% resistance=39k package=THT]
  R5 = Resistor [tolerance=±5% resistance=220 package=THT]
  C1 = Ceramic Capacitor [capacitance=0.1µF voltage=16V package="200 mil [THT, multilayer]"]
  R7 = Resistor [tolerance=±5% resistance=10M package=THT]
  R8 = Resistor [tolerance=±5% resistance=4.7M package=THT]
  8x_AA_or_3x_18606 = DC Power [voltage=12V]
  U2 = V_REG_LD1117VXX [part_number="3.3V Switching step-down, e.g. Pololu D24V5F3" package=78xxl]
  LED1 = DUO LED RG [package="5 mm [THT]"]
  R6 = Resistor [tolerance=±5% resistance=150 package=THT]
  R9 = Resistor [tolerance=±5% resistance=160k package=THT]
  R10 = Resistor [tolerance=±5% resistance=160k package=THT]
  R11 = Resistor [tolerance=±5% resistance=160k package=THT]

nets:
  N1: U1.connector0, R2.Pin_1, R5.Pin_0, R7.Pin_1
  N2: U1.connector1, R3.Pin_0, R4.Pin_1
  N3: U1.connector2, R1.Pin_1, R2.Pin_0
  GND: U1.connector3, R4.Pin_0, C1.0, 8x_AA_or_3x_18606.V-, U2.GND, R10.Pin_0
  N4: U1.connector4, R9.Pin_0, R10.Pin_1, R11.Pin_0
  N5: U1.connector5, C1.1, R7.Pin_0, R8.Pin_0
  N6: U1.connector6, R8.Pin_1, R6.Pin_0, R11.Pin_1
  N7: U1.connector7, R3.Pin_1, 8x_AA_or_3x_18606.V+, U2.IN
  N8: R1.Pin_0, U2.OUT, LED1.common_cathode, R9.Pin_1
  N9: R5.Pin_1, LED1.green_anode
  N10: LED1.red_anode, R6.Pin_1

notes:
  Power Indicator, Power on and low battery indicator.  Glows green if battery voltage >8.9V.   Blinks red otherwise., 0.3
  With 3.3V switching step-down, total current consumed is kept under 5mA at all battery voltages.
