# Fritzing sketch id855_Robotitos_0 (saved by Fritzing 0.8.3b)
circuit board: 6.34527cm x 2.77988cm
breadboards: 1

parts:
  MIC = Microphone
  R1 = Resistor [tolerance=±5% resistance=12k package=THT]
  C1 = Ceramic Capacitor [capacitance=100nF package="100 mil [THT, multilayer]"]
  Q1 = NPN-Transistor [package="TO92 [THT]"]
  R2 = Resistor [tolerance=±5% resistance=100k package=THT]
  R3 = Resistor [tolerance=±5% resistance=15k package=THT]
  C2 = Ceramic Capacitor [capacitance=100nF package="100 mil [THT, multilayer]"]
  VCC1 = Battery block 9V
  Parte1 = Arduino Uno (Rev3)
  R4 = Resistor [tolerance=±5% resistance=220 package=THT]
  R5 = Photocell (LDR) [package=THT]
  SPKR1 = Loudspeaker
  R6 = Resistor [tolerance=±5% resistance=1k package=THT]
  LED1 = LED - 5mm [color="White (4500K)" package="5 mm [THT]"]
  LED2 = LED - 5mm [color="White (4500K)" package="5 mm [THT]"]
  LED3 = LED - 5mm [color="White (4500K)" package="5 mm [THT]"]
  LED4 = LED - 5mm [color="White (4500K)" package="5 mm [THT]"]
  R7 = Resistor [tolerance=±5% resistance=300 package=THT]
  R8 = Resistor [tolerance=±5% resistance=300 package=THT]
  R9 = Resistor [tolerance=±5% resistance=300 package=THT]
  R10 = Resistor [tolerance=±5% resistance=300 package=THT]

nets:
  N1: MIC.pin1, R1.Pin_0, C1.1
  N2: MIC.pin2, Q1.E, Parte1.GND, R4.Pin_1, SPKR1.pin2, LED1.cathode, LED2.cathode, LED3.cathode, LED4.cathode
  N3: R1.Pin_1, R3.Pin_0, VCC1.+
  N4: C1.0, Q1.B, R2.Pin_0
  N5: Q1.C, R2.Pin_1, R3.Pin_1, C2.1
  N6: C2.0, Parte1.A0
  GND: VCC1.-
  N7: Parte1.A1, R4.Pin_0, R5.pin_1
  N8: Parte1.5V, R5.pin_0
  N9: Parte1.D8, R6.Pin_0
  N10: Parte1.D9_PWM, R8.Pin_0
  N11: Parte1.D10_PWM/SS, R7.Pin_0
  N12: Parte1.D5_PWM, R10.Pin_0
  N13: Parte1.D6_PWM, R9.Pin_0
  N14: SPKR1.pin1, R6.Pin_1
  N15: LED1.anode, R7.Pin_1
  N16: LED2.anode, R8.Pin_1
  N17: LED3.anode, R9.Pin_1
  N18: LED4.anode, R10.Pin_1
