# Fritzing sketch id857_1WELCOME_LICEO_JACKUntitled_Sketch_2_0 (saved by Fritzing 0.9.3b)
breadboards: 1

parts:
  Componente1 = Arduino Uno (Rev3)
  RE1 = Rotary Encoder [package=THT]
  LCD1 = LCD screen

nets:
  N1: Componente1.D11_PWM/MOSI, LCD1.E
  N2: Componente1.D12/MISO, LCD1.RS
  N3: Componente1.D2, Componente1.D3_PWM, LCD1.DB6
  N4: Componente1.D4, LCD1.DB5
  N5: Componente1.D5_PWM, LCD1.DB4
  5V: Componente1.5V, RE1.EncoderPinB, LCD1.VDD, LCD1.LED+
  GND: Componente1.GND, RE1.EncoderPinA, LCD1.VSS, LCD1.R/W, LCD1.LED-
  N6: RE1.EncoderPinC, LCD1.V0
