# Fritzing sketch id858_big_muff_V3_by_Nc333_0 (saved by Fritzing 0.8.7b)
circuit board: 8.15688cm x 4.27484cm
breadboards: 1

parts:
  C9 = Ceramic Capacitor [capacitance=4nF package="100 mil [THT, multilayer]"]
  R4 = Resistor [tolerance=±5% resistance=3.3k package=THT]
  R23 = Resistor [tolerance=±5% resistance=1k package=THT]
  C13 = Ceramic Capacitor [capacitance=0.1µF package="100 mil [THT, multilayer]"]
  R15 = Resistor [tolerance=±5% resistance=470k package=THT]
  R27 = Resistor [tolerance=±5% resistance=15k package=THT]
  R13 = Resistor [tolerance=±5% resistance=15k package=THT]
  R11 = Resistor [tolerance=±5% resistance=15k package=THT]
  Q2 = NPN-Transistor [package="TO92 [THT]"]
  Q4 = NPN-Transistor [part_number=BC239 package="TO92 [THT]"]
  R18 = Resistor [tolerance=±5% resistance=15k package=THT]
  R10 = Resistor [tolerance=±5% resistance=150 package=THT]
  Q3 = NPN-Transistor [package="TO92 [THT]"]
  C8 = Ceramic Capacitor [capacitance=0.01µF voltage=0.1kV package="100 mil [THT, multilayer]"]
  R8 = Resistor [tolerance=±5% resistance=39k package=THT]
  C11 = Ceramic Capacitor [capacitance=470pF package="100 mil [THT, multilayer]"]
  C1 = Tantalum Capacitor [capacitance=10µF voltage=10V package="100 mil [THT, tantalum]"]
  C12 = Ceramic Capacitor [capacitance=470pF package="100 mil [THT, multilayer]"]
  R5 = Resistor [tolerance=±5% resistance=22 package=THT]
  C3 = Ceramic Capacitor [capacitance=0.1µF package="100 mil [THT, multilayer]"]
  C10 = Ceramic Capacitor [capacitance=470pF package="100 mil [THT, multilayer]"]
  D2 = Rectifier Diode [part_number=1N914 package="300 mil [THT]"]
  C5 = Tantalum Capacitor [capacitance=1μF package="100 mil [THT, tantalum]"]
  R19 = Resistor [tolerance=±5% resistance=10k part_number="also 10k6" package=THT]
  Q1 = NPN-Transistor [package="TO92 [THT]"]
  C4 = Ceramic Capacitor [capacitance=1µF package="100 mil [THT, multilayer]"]
  R2 = Resistor [tolerance=±5% resistance=39k package=THT]
  D1 = Rectifier Diode [part_number=1N914 package="300 mil [THT]"]
  R15_2 = Resistor [tolerance=±5% resistance=470k package=THT]
  D3 = Rectifier Diode [part_number=1N914 package="300 mil [THT]"]
  R14 = Resistor [tolerance=±5% resistance=47k package=THT]
  C2 = Tantalum Capacitor [capacitance=100nF package="100 mil [THT, tantalum]"]
  R10_2 = Resistor [tolerance=±5% resistance=100k package=THT]
  C5_2 = Ceramic Capacitor [capacitance=0.1µF package="100 mil [THT, multilayer]"]
  R26 = Resistor [tolerance=±5% resistance=220 package=THT]
  R22 = Resistor [tolerance=±5% resistance=100 package=THT]
  R12 = Resistor [tolerance=±5% resistance=10k part_number="also 10K6" package=THT]
  D4 = Rectifier Diode [part_number=1N914 package="300 mil [THT]"]
  R7 = Resistor [tolerance=±5% resistance=430k package=THT]
  R9 = Resistor [tolerance=±5% resistance=470k package=THT]
  R16 = Resistor [tolerance=±5% resistance=100k package=THT]
  R24 = Rotary Potentiometer (Large) [maximum_resistance=100kΩ part_number=Sustain package=THT]
  R25 = Rotary Potentiometer (Large) [maximum_resistance=100kΩ package=THT]
  R28 = Rotary Potentiometer (Large) [maximum_resistance=100kΩ package=THT]
  J1 = Power Jack [package=power_jack_slot]
  MASSE1 = Header 1 [part_number=In package=snap-male]
  MASSE2 = Header 1 [part_number=Out package=snap-male]
  SIGNAL = Header 1 [part_number=In package=snap-male]
  MASSE = Header 1 [part_number=Out package=snap-male]
  SIGNAL_OUT = Header 1 [part_number=Out package=snap-male]

nets:
  N1: C9.0, R15.Pin_1, R11.Pin_1, Q2.C, R8.Pin_0, C11.1, D2.anode, D1.cathode
  N2: C9.1, R5.Pin_1, R25.leg1
  N3: R4.Pin_0, Q1.E
  N4: R4.Pin_1, R23.Pin_0, R10.Pin_1, C8.0, R5.Pin_0, R14.Pin_1, R10_2.Pin_1, R26.Pin_0, R22.Pin_1, R16.Pin_1, R28.leg1, MASSE2.1, MASSE.1
  N5: R23.Pin_1, R24.leg1
  N6: C13.0, Q3.E
  N7: C13.1, R12.Pin_0
  N8: R15.Pin_0, Q2.B, C11.0, D2.cathode, D1.anode, R12.Pin_1, R16.Pin_0
  N9: R27.Pin_0, R11.Pin_0, R18.Pin_1, Q3.C, C12.0, R15_2.Pin_1, D3.anode, D4.cathode, R7.Pin_0
  N10: R27.Pin_1, Q1.C, C2.-
  N11: R13.Pin_0, R18.Pin_0, J1.GNDBREAK, J1.GND
  N12: R13.Pin_1, Q4.C, R9.Pin_1
  N13: Q2.E, R10.Pin_0
  N14: Q4.E, R22.Pin_0
  N15: Q4.B, C1.+, C10.1, R14.Pin_0, R9.Pin_0
  N16: Q3.B, C12.1, C5.-, R19.Pin_1, R15_2.Pin_0, R10_2.Pin_0
  N17: C8.1, R8.Pin_1, R25.leg2
  N18: C1.-, R2.Pin_1
  N19: C3.0, R25.wiper
  N20: C3.1, Q1.B, R26.Pin_1, R7.Pin_1
  N21: C10.0, C4.1
  N22: C5.+, D3.cathode, D4.anode
  N23: R19.Pin_0, C5_2.1
  N24: C4.0, R24.leg2
  N25: R2.Pin_0, SIGNAL.1
  N26: C2.+, R28.leg2
  N27: C5_2.0, R24.wiper
  N28: R28.wiper, SIGNAL_OUT.1
  N29: J1.PWR, MASSE1.1

notes:
  Big muff V3 by nc333
  Big muff V.3 by Nc333
  all right to Electro harmonix (r)
  Signal Out
  Signal in
