# Fritzing sketch id859_BigBen_0 (saved by Fritzing 0.7.11b)
breadboards: 1

parts:
  C1 = Ceramic Capacitor [capacitance=10nF package="100 mil [THT, multilayer]"]
  R1 = Resistor [tolerance=±5% resistance=12k package=THT]
  C2 = Electrolytic Capacitor [capacitance=1µF package="100 mil [THT, electrolytic]"]
  IC2 = IC, DIP package, 40 pins [chip_label=XuLA2-LX25]

nets:
  N1: C1.0, R1.Pin_0, C2.+
  N2: C1.1, IC2.pin18
  N3: R1.Pin_1, IC2.pin3

notes:
  to audio
  amplifier
  to PC (via USB)
