# Fritzing sketch id85_2led_1switch_Ft_0 (saved by Fritzing 0.9.2b)
breadboards: 1

parts:
  S1 = Pushbutton [package="[THT]"]
  R1 = Resistor [tolerance=±5% resistance=10k package=THT]
  R2 = Resistor [tolerance=±5% resistance=100 package=THT]
  Part1 = Arduino Uno (Rev3)
  R3 = Resistor [tolerance=±5% resistance=330 package=THT]  # not connected
  LED2 = LED - 5mm [color="Red (633nm)" package="5 mm [THT]"]
  R4 = Resistor [tolerance=±5% resistance=330 package=THT]
  LED3 = LED - 5mm [color="Red (633nm)" package="5 mm [THT]"]

nets:
  N1: S1.Pin_1, S1.Pin_2, R1.Pin_0, R2.Pin_0
  N2: S1.Pin_3, S1.Pin_4, Part1.GND, LED2.cathode, LED3.cathode
  N3: R1.Pin_1, Part1.5V
  N4: R2.Pin_1, Part1.D2
  N5: Part1.D12/MISO, R4.Pin_1
  N6: LED2.anode, R4.Pin_0

notes:
  10 KΩ
  100Ω
  330Ω
