# Fritzing sketch id860_BigRedButton_0 (saved by Fritzing 0.9.3b)
breadboards: 1

parts:
  S1 = Round Pushbutton
  S2 = Toggle Switch [package=THT]
  Part1 = Arduino Uno (Rev3)
  LED1 = smd LED [color="Red (633nm)" package="0805 [SMD]"]
  R2 = Resistor [tolerance=±5% resistance=220 package=THT]
  R3 = Resistor [tolerance=±5% resistance=220 package=THT]

nets:
  N1: S1.leg0, Part1.D3_PWM, R3.Pin_0
  N2: S1.leg1, S2.L1, Part1.5V
  N3: S2.L2, Part1.D2, R2.Pin_0
  N4: Part1.D13/SCK, LED1.anode
  N5: Part1.GND, LED1.cathode, R2.Pin_1, R3.Pin_1
