# Fritzing sketch id861_First_testing_0 (saved by Fritzing 0.9.3b)
breadboards: 2

parts:
  Part1 = Bluetooth HC-05 Macho
  Part2 = Arduino Uno (Rev3)
  LCD1 = LCD screen
  SERVO1 = Adafruit_Feedback_Servo__small
  LCM1602_IIC2 = generic_ic_dip_22_300mil.fzp [part_number="LCM1602 IIC" chip_label="LCM1602 IIC"]
  8_Channel_Relay1 = richardbruneau00
  R1 = Resistor [tolerance=±2% resistance=4.7k package=THT]
  R2 = Resistor [tolerance=±2% resistance=2k package=THT]
  Q1 = prefix0000  # not connected
  S1 = Momentary Switch [package=ksa_sealed_tac_switch]
  R3 = Resistor [tolerance=±2% resistance=10k package=THT]

nets:
  N1: Part1.TXD, Part2.D0/RX
  N2: Part1.RXD, R1.Pin_0, R2.Pin_0
  VCC: Part1.VCC, Part2.5V, SERVO1.connector3, LCM1602_IIC2.connector17, 8_Channel_Relay1.connector17, S1.4
  GND: Part1.GND, Part2.GND, SERVO1.connector4, LCM1602_IIC2.connector16, 8_Channel_Relay1.connector8, R1.Pin_1, R3.Pin_0
  N3: Part2.A4/SDA, LCM1602_IIC2.connector18
  N4: Part2.A5/SCL, LCM1602_IIC2.connector19
  N5: Part2.D10_PWM/SS, 8_Channel_Relay1.connector9
  N6: Part2.D11_PWM/MOSI, 8_Channel_Relay1.connector10
  N7: Part2.D12/MISO, 8_Channel_Relay1.connector11
  N8: Part2.D1/TX, R2.Pin_1
  N9: Part2.D2, S1.1
  N10: Part2.D3_PWM, SERVO1.connector2
  N11: LCD1.VSS, LCM1602_IIC2.connector0
  N12: LCD1.VDD, LCM1602_IIC2.connector1
  N13: LCD1.V0, LCM1602_IIC2.connector2
  N14: LCD1.RS, LCM1602_IIC2.connector3
  N15: LCD1.R/W, LCM1602_IIC2.connector4
  N16: LCD1.E, LCM1602_IIC2.connector5
  N17: LCD1.DB0, LCM1602_IIC2.connector6
  N18: LCD1.DB1, LCM1602_IIC2.connector7
  N19: LCD1.DB2, LCM1602_IIC2.connector8
  N20: LCD1.DB3, LCM1602_IIC2.connector9
  N21: LCD1.DB4, LCM1602_IIC2.connector10
  N22: LCD1.DB5, LCM1602_IIC2.connector11
  N23: LCD1.DB6, LCM1602_IIC2.connector12
  N24: LCD1.DB7, LCM1602_IIC2.connector13
  N25: LCD1.LED+, LCM1602_IIC2.connector14
  N26: LCD1.LED-, LCM1602_IIC2.connector15
  N27: LCM1602_IIC2.connector20, LCM1602_IIC2.connector21
  N28: 8_Channel_Relay1.connector19, 8_Channel_Relay1.connector20
  N29: 8_Channel_Relay1.connector21, 8_Channel_Relay1.connector24, 8_Channel_Relay1.connector27
  N30: S1.2, R3.Pin_1
