# Fritzing sketch id862_Binary_clock_prototype_0 (saved by Fritzing 0.9.3b)
breadboards: 1

parts:
  LED1 = LED - 5mm [color="Blue (525nm)" package="5 mm [THT]"]
  LED2 = LED - 5mm [color="Orange (620nm)" package="5 mm [THT]"]
  LED3 = LED - 5mm [color="Orange (620nm)" package="5 mm [THT]"]
  LED4 = LED - 5mm [color="Orange (620nm)" package="5 mm [THT]"]
  LED5 = LED - 5mm [color="Orange (620nm)" package="5 mm [THT]"]
  R1 = Resistor [tolerance=±5% resistance=220 package=THT]
  R2 = Resistor [tolerance=±5% resistance=220 package=THT]
  R3 = Resistor [tolerance=±5% resistance=220 package=THT]
  R4 = Resistor [tolerance=±5% resistance=220 package=THT]
  R5 = Resistor [tolerance=±5% resistance=220 package=THT]
  R6 = Resistor [tolerance=±5% resistance=220 package=THT]
  LED6 = LED - 5mm [color="Orange (620nm)" package="5 mm [THT]"]
  Part1 = Arduino Nano (Rev3.0)
  LED7 = LED - 5mm [color="Green (555nm)" package="5 mm [THT]"]
  LED8 = LED - 5mm [color="Green (555nm)" package="5 mm [THT]"]
  LED9 = LED - 5mm [color="Green (555nm)" package="5 mm [THT]"]
  LED10 = LED - 5mm [color="Green (555nm)" package="5 mm [THT]"]
  LED11 = LED - 5mm [color="Green (555nm)" package="5 mm [THT]"]
  LED12 = LED - 5mm [color="Green (555nm)" package="5 mm [THT]"]
  R7 = Resistor [tolerance=±5% resistance=220 package=THT]
  R8 = Resistor [tolerance=±5% resistance=220 package=THT]
  R9 = Resistor [tolerance=±5% resistance=220 package=THT]
  R10 = Resistor [tolerance=±5% resistance=220 package=THT]
  R11 = Resistor [tolerance=±5% resistance=220 package=THT]
  R12 = Resistor [tolerance=±5% resistance=220 package=THT]
  ZS-042_RTC1 = ZS-042 RTC Module

nets:
  N1: LED1.cathode, R1.Pin_1
  N2: LED1.anode, Part1.D13/SCK
  N3: LED2.cathode, R2.Pin_1
  N4: LED2.anode, Part1.D6
  N5: LED3.cathode, R3.Pin_1
  N6: LED3.anode, Part1.D5
  N7: LED4.cathode, R4.Pin_1
  N8: LED4.anode, Part1.D4
  N9: LED5.cathode, R5.Pin_1
  N10: LED5.anode, Part1.D3
  GND: R1.Pin_0, R2.Pin_0, R3.Pin_0, R4.Pin_0, R5.Pin_0, R6.Pin_0, Part1.GND, R7.Pin_1, R9.Pin_1, R10.Pin_1, R12.Pin_1, ZS-042_RTC1.GND
  N11: R6.Pin_1, LED6.cathode
  N12: LED6.anode, Part1.D2
  N13: Part1.D7, LED12.anode
  N14: Part1.D8, LED11.anode
  N15: Part1.D9, LED10.anode
  N16: Part1.D10, LED9.anode
  N17: Part1.D11/MOSI, LED8.anode
  N18: Part1.D12/MISO, LED7.anode
  5V: Part1.5V, ZS-042_RTC1.VCC
  N19: Part1.A5, ZS-042_RTC1.SCL
  N20: Part1.A4, ZS-042_RTC1.SDA
  N21: LED7.cathode, R7.Pin_0
  N22: LED8.cathode, R8.Pin_0
  N23: LED9.cathode, R9.Pin_0
  N24: LED10.cathode, R10.Pin_0
  N25: LED11.cathode, R11.Pin_0
  N26: LED12.cathode, R12.Pin_0
