# Fritzing sketch id863_Binary_Clock_DS1307_Perfboard_0 (saved by Fritzing 0.8.7b)
stripboards: 3

parts:
  LED25 = LED - 3mm [color="Blue (505nm)" package="3 mm [THT]"]
  LED26 = LED - 3mm [color="Blue (505nm)" package="3 mm [THT]"]
  LED27 = LED - 3mm [color="Blue (505nm)" package="3 mm [THT]"]
  LED28 = LED - 3mm [color="Blue (505nm)" package="3 mm [THT]"]
  LED29 = LED - 3mm [color="Blue (505nm)" package="3 mm [THT]"]
  LED30 = LED - 3mm [color="Blue (505nm)" package="3 mm [THT]"]
  LED31 = LED - 3mm [color="Blue (505nm)" package="3 mm [THT]"]
  LED32 = LED - 3mm [color="Blue (505nm)" package="3 mm [THT]"]
  LED33 = LED - 3mm [color="Blue (505nm)" package="3 mm [THT]"]
  LED34 = LED - 3mm [color="Blue (505nm)" package="3 mm [THT]"]
  LED35 = LED - 3mm [color="Blue (505nm)" package="3 mm [THT]"]
  LED36 = LED - 3mm [color="Blue (505nm)" package="3 mm [THT]"]
  LED37 = LED - 3mm [color="Blue (505nm)" package="3 mm [THT]"]
  LED38 = LED - 3mm [color="Blue (505nm)" package="3 mm [THT]"]
  LED39 = LED - 3mm [color="Blue (505nm)" package="3 mm [THT]"]
  LED40 = LED - 3mm [color="Blue (505nm)" package="3 mm [THT]"]
  LED41 = LED - 3mm [color="Blue (505nm)" package="3 mm [THT]"]
  LED42 = LED - 3mm [color="Blue (505nm)" package="3 mm [THT]"]
  LED43 = LED - 3mm [color="Blue (505nm)" package="3 mm [THT]"]
  LED44 = LED - 3mm [color="Blue (505nm)" package="3 mm [THT]"]
  LED45 = LED - 3mm [color="Blue (505nm)" package="3 mm [THT]"]
  LED46 = LED - 3mm [color="Blue (505nm)" package="3 mm [THT]"]
  LED47 = LED - 3mm [color="Blue (505nm)" package="3 mm [THT]"]
  LED48 = LED - 3mm [color="Blue (505nm)" package="3 mm [THT]"]
  IC4 = MICROCONTROLLER [package=dil28-3-simon-kit]
  IC5 = DS1307 [package=THT]
  74HC2 = 74HC164
  Q11 = TRANSISTOR_NPN [package=to-92-ammo]
  Q12 = TRANSISTOR_NPN [package=to-92-ammo]
  R11 = Resistor [tolerance=±5% resistance=10k package=THT]
  U3 = POT [package=trim_pot]
  R18 = Photocell (LDR) [package=THT]
  S5 = Momentary Switch [package=ksa_sealed_tac_switch]
  S6 = Momentary Switch [package=ksa_sealed_tac_switch]
  R19 = Resistor [tolerance=±5% resistance=100k package=THT]
  C1 = Ceramic Capacitor [capacitance=20pF package="1206 [SMD, multilayer]"]
  C2 = Ceramic Capacitor [capacitance=20pF package="1206 [SMD, multilayer]"]
  R20 = Resistor [tolerance=±5% resistance=10k package=THT]
  R21 = Resistor [tolerance=±5% resistance=10k package=THT]
  R22 = Resistor [tolerance=±5% resistance=10k package=THT]
  Q14 = TRANSISTOR_NPN [package=to-92-ammo]
  R23 = Resistor [tolerance=±5% resistance=100 package=THT]
  R24 = Resistor [tolerance=±5% resistance=100 package=THT]
  R25 = Resistor [tolerance=±5% resistance=100 package=THT]
  R26 = Resistor [tolerance=±5% resistance=100 package=THT]
  R27 = Resistor [tolerance=±5% resistance=100 package=THT]
  R28 = Resistor [tolerance=±5% resistance=100 package=THT]
  Q20 = TRANSISTOR_NPN [package=to-92-ammo]
  Q21 = TRANSISTOR_NPN [package=to-92-ammo]
  Q22 = TRANSISTOR_NPN [package=to-92-ammo]
  Q23 = TRANSISTOR_NPN [package=to-92-ammo]
  Q24 = TRANSISTOR_NPN [package=to-92-ammo]
  Q25 = TRANSISTOR_NPN [package=to-92-ammo]
  Q26 = TRANSISTOR_NPN [package=to-92-ammo]
  Q27 = TRANSISTOR_NPN [package=to-92-ammo]
  Q28 = TRANSISTOR_NPN [package=to-92-ammo]
  R29 = Resistor [tolerance=±5% resistance=10k package=THT]
  BAT5 = Battery Holders [package=battcom_20mm_pth]
  X3 = USB Connectors [package=usb-b-smt]
  R30 = Resistor [tolerance=±5% resistance=100k package=THT]
  XTAL3 = Crystal [frequency="16 Mhz" package=THT]
  Y3 = CRYSTAL [package=crystal-32khz-smd]

nets:
  N1: LED25.cathode, LED28.cathode, LED29.cathode, LED38.cathode, LED43.cathode, LED47.cathode, Q28.E
  N2: LED25.anode, LED30.anode, LED40.anode, LED46.anode
  N3: LED26.cathode, LED27.cathode, LED31.cathode, LED36.cathode, LED40.cathode, LED42.cathode, Q27.E
  N4: LED26.anode, LED34.anode, LED38.anode, LED39.anode
  N5: LED27.anode, LED28.anode, LED32.anode, LED45.anode
  N6: LED29.anode, LED33.anode, LED36.anode, LED48.anode
  N7: LED30.cathode, LED37.cathode, LED39.cathode, LED44.cathode, LED45.cathode, LED48.cathode, Q14.E
  N8: LED31.anode, LED37.anode, LED41.anode, LED47.anode
  N9: LED32.cathode, LED33.cathode, LED34.cathode, LED35.cathode, LED41.cathode, LED46.cathode, Q26.E
  N10: LED35.anode, LED42.anode, LED43.anode, LED44.anode
  N11: IC4.PC6(_RESET), R29.Pin_1
  N12: IC4.PD0(RXD), 74HC2.connector1
  N13: IC4.PD1(TXD), 74HC2.connector7
  N14: IC4.PD2(INT0), S5.4
  N15: IC4.PD3(INT1), S6.4
  N16: IC4.VCC, IC4.AVCC, IC5.+V, 74HC2.connector0, 74HC2.connector9, Q11.C, U3.S, U3.E, R18.pin_1, R19.Pin_1, X3.VBUS, R30.Pin_1
  GND: IC4.GND, IC4.AGND, IC5.0V, 74HC2.connector6, S5.2, S6.2, C1.1, C2.1, BAT5.-, X3.GND
  N17: IC4.PB6(XTAL1_TOSC1), C1.0, XTAL3.pin_0
  N18: IC4.PB7(XTAL2_TOSC2), C2.0, XTAL3.pin_1
  N19: IC4.PC4(ADC4_SDA), IC5.SDA_-_I2C_Data
  N20: IC4.PC5(ADC5_SCL), IC5.SCL_-_I2C_Clock
  N21: IC5.X1_-_Crystal, Y3.2
  N22: IC5.X2_-_Crystal, Y3.1
  N23: IC5.Vbat_-_Backup_Supply, BAT5.+
  N24: Q11.E, Q12.C
  N25: Q12.E, R11.Pin_1, R20.Pin_1, R21.Pin_1, R22.Pin_1
  N26: Q12.B, R18.pin_0
  N27: R11.Pin_0, Q28.B
  N28: S5.3, R30.Pin_0
  N29: S6.3, R19.Pin_0
  N30: R20.Pin_0, Q27.B
  N31: R21.Pin_0, Q26.B
  N32: R22.Pin_0, Q14.B
  N33: R23.Pin_0, Q20.B
  N34: R24.Pin_0, Q21.B
  N35: R25.Pin_0, Q23.B
  N36: R26.Pin_0, Q22.B
  N37: R27.Pin_0, Q25.B
  N38: R28.Pin_0, Q24.B
  N39: Q20.E, Q21.E, Q22.E, Q23.E, Q24.E, Q25.E
