# Fritzing sketch id864_reloj_leds_0 (saved by Fritzing 0.9.2b)
circuit board: 21.6516cm x 7.3127cm
breadboards: 3

parts:
  Parte1 = Arduino Uno (Rev3)
  U1 = 74HC595 [package="DIP16 [THT]"]
  Parte2 = Real Time Clock Module - DS1307 RTC Breakout Board
  R1 = Resistor [tolerance=±5% resistance=220 package=THT]
  R2 = Resistor [tolerance=±5% resistance=220 package=THT]
  R3 = Resistor [tolerance=±5% resistance=220 package=THT]
  R4 = Resistor [tolerance=±5% resistance=220 package=THT]
  R5 = Resistor [tolerance=±5% resistance=220 package=THT]
  R6 = Resistor [tolerance=±5% resistance=220 package=THT]
  R7 = Resistor [tolerance=±5% resistance=220 package=THT]
  R8 = Resistor [tolerance=±5% resistance=220 package=THT]
  U4 = 74HC595 [package="DIP16 [THT]"]
  R9 = Resistor [tolerance=±5% resistance=220 package=THT]
  R10 = Resistor [tolerance=±5% resistance=220 package=THT]
  R11 = Resistor [tolerance=±5% resistance=220 package=THT]
  R12 = Resistor [tolerance=±5% resistance=220 package=THT]
  R13 = Resistor [tolerance=±5% resistance=220 package=THT]
  R14 = Resistor [tolerance=±5% resistance=220 package=THT]
  R15 = Resistor [tolerance=±5% resistance=220 package=THT]
  R16 = Resistor [tolerance=±5% resistance=220 package=THT]
  U5 = 74HC595 [package="DIP16 [THT]"]
  R17 = Resistor [tolerance=±5% resistance=220 package=THT]
  R18 = Resistor [tolerance=±5% resistance=220 package=THT]
  R19 = Resistor [tolerance=±5% resistance=220 package=THT]
  R20 = Resistor [tolerance=±5% resistance=220 package=THT]
  R21 = Resistor [tolerance=±5% resistance=220 package=THT]
  R22 = Resistor [tolerance=±5% resistance=220 package=THT]
  R23 = Resistor [tolerance=±5% resistance=220 package=THT]
  R24 = Resistor [tolerance=±5% resistance=220 package=THT]
  LED5 = LED - 3mm [color="Red (633nm)" package="3 mm [THT]"]
  LED17 = LED - 3mm [color="Red (633nm)" package="3 mm [THT]"]
  LED22 = LED - 3mm [color="Red (633nm)" package="3 mm [THT]"]
  LED18 = LED - 3mm [color="Red (633nm)" package="3 mm [THT]"]
  LED19 = LED - 3mm [color="Red (633nm)" package="3 mm [THT]"]
  LED20 = LED - 3mm [color="Red (633nm)" package="3 mm [THT]"]
  LED21 = LED - 3mm [color="Red (633nm)" package="3 mm [THT]"]
  LED23 = LED - 3mm [color="Red (633nm)" package="3 mm [THT]"]
  LED24 = LED - 3mm [color="Red (633nm)" package="3 mm [THT]"]
  LED2 = LED - 3mm [color="Red (633nm)" package="3 mm [THT]"]
  LED1 = LED - 3mm [color="Red (633nm)" package="3 mm [THT]"]
  LED3 = LED - 3mm [color="Red (633nm)" package="3 mm [THT]"]
  LED4 = LED - 3mm [color="Red (633nm)" package="3 mm [THT]"]
  LED7 = LED - 3mm [color="Red (633nm)" package="3 mm [THT]"]
  LED6 = LED - 3mm [color="Red (633nm)" package="3 mm [THT]"]
  LED8 = LED - 3mm [color="Red (633nm)" package="3 mm [THT]"]
  LED9 = LED - 3mm [color="Red (633nm)" package="3 mm [THT]"]
  LED10 = LED - 3mm [color="Red (633nm)" package="3 mm [THT]"]
  LED11 = LED - 3mm [color="Red (633nm)" package="3 mm [THT]"]
  LED12 = LED - 3mm [color="Red (633nm)" package="3 mm [THT]"]
  LED13 = LED - 3mm [color="Red (633nm)" package="3 mm [THT]"]
  LED15 = LED - 3mm [color="Red (633nm)" package="3 mm [THT]"]
  LED14 = LED - 3mm [color="Red (633nm)" package="3 mm [THT]"]
  LED16 = LED - 3mm [color="Red (633nm)" package="3 mm [THT]"]
  S1 = Pushbutton [package=THT]  # not connected
  S2 = Pushbutton [package=THT]  # not connected
  S3 = Pushbutton [package=THT]  # not connected
  R26 = Resistor [tolerance=±5% resistance=220 package=THT]  # not connected
  R27 = Resistor [tolerance=±5% resistance=220 package=THT]  # not connected

nets (from the breadboard view):
  N1: Parte1.D8, U1.ST_CP
  N2: Parte1.D9_PWM, U1.DS
  N3: Parte1.D10_PWM/SS, U5.SH_CP
  N4: Parte1.D11_PWM/MOSI, U5.DS
  N5: Parte1.D12/MISO, U5.ST_CP
  GND: Parte1.GND, U1.GND, U1.OE, Parte2.GND, U4.GND, U4.OE, U5.GND, U5.OE, LED5.anode, LED17.anode, LED22.anode, LED18.anode, LED19.anode, LED20.anode, LED21.anode, LED23.anode, LED24.anode, LED2.anode, LED1.anode, LED3.anode, LED4.anode, LED7.anode, LED6.anode, LED8.anode, LED9.anode, LED10.anode, LED11.anode, LED12.anode, LED13.anode, LED15.anode, LED14.anode, LED16.anode
  N6: Parte1.D3_PWM, U4.DS
  N7: Parte1.D4, U4.ST_CP
  N8: Parte1.D5_PWM, U4.SH_CP
  N9: Parte1.D6_PWM, U1.SH_CP
  VCC: Parte1.5V, U1.MR, U1.VCC, Parte2.5V, U4.MR, U4.VCC, U5.MR, U5.VCC
  N10: U1.Q1, R1.Pin_0
  N11: U1.Q2, R2.Pin_0
  N12: U1.Q3, R3.Pin_0
  N13: U1.Q4, R4.Pin_0
  N14: U1.Q5, R5.Pin_0
  N15: U1.Q6, R6.Pin_0
  N16: U1.Q7, R7.Pin_0
  N17: U1.Q0, R8.Pin_0
  N18: R1.Pin_1, LED1.cathode
  N19: R2.Pin_1, LED2.cathode
  N20: R3.Pin_1, LED3.cathode
  N21: R4.Pin_1, LED4.cathode
  N22: R5.Pin_1, LED5.cathode
  N23: R6.Pin_1, LED6.cathode
  N24: R7.Pin_1, LED7.cathode
  N25: R8.Pin_1, LED8.cathode
  N26: U4.Q1, R13.Pin_0
  N27: U4.Q2, R14.Pin_0
  N28: U4.Q3, R11.Pin_0
  N29: U4.Q4, R16.Pin_0
  N30: U4.Q5, R9.Pin_0
  N31: U4.Q6, R12.Pin_0
  N32: U4.Q7, R15.Pin_0
  N33: U4.Q0, R10.Pin_0
  N34: R9.Pin_1, LED13.cathode
  N35: R10.Pin_1, LED16.cathode
  N36: R11.Pin_1, LED11.cathode
  N37: R12.Pin_1, LED14.cathode
  N38: R13.Pin_1, LED9.cathode
  N39: R14.Pin_1, LED10.cathode
  N40: R15.Pin_1, LED15.cathode
  N41: R16.Pin_1, LED12.cathode
  N42: U5.Q1, R21.Pin_0
  N43: U5.Q2, R22.Pin_0
  N44: U5.Q3, R19.Pin_0
  N45: U5.Q4, R24.Pin_0
  N46: U5.Q5, R17.Pin_0
  N47: U5.Q6, R20.Pin_0
  N48: U5.Q7, R23.Pin_0
  N49: U5.Q0, R18.Pin_0
  N50: R17.Pin_1, LED21.cathode
  N51: R18.Pin_1, LED24.cathode
  N52: R19.Pin_1, LED19.cathode
  N53: R20.Pin_1, LED22.cathode
  N54: R21.Pin_1, LED17.cathode
  N55: R22.Pin_1, LED18.cathode
  N56: R23.Pin_1, LED23.cathode
  N57: R24.Pin_1, LED20.cathode
