# Fritzing sketch id865_Binary_Clock_Build_0 (saved by Fritzing 0.9.3b)
breadboards: 1

parts:
  Bauteil1 = Arduino Uno (Rev3)
  LED1 = LED - 5mm [color="Red (633nm)" package="5 mm [THT]"]
  LED2 = LED - 5mm [color="Red (633nm)" package="5 mm [THT]"]
  LED3 = LED - 5mm [color="Red (633nm)" package="5 mm [THT]"]
  LED4 = LED - 5mm [color="Red (633nm)" package="5 mm [THT]"]
  LED5 = LED - 5mm [color="Yellow (592nm)" package="5 mm [THT]"]
  LED6 = LED - 5mm [color="Yellow (592nm)" package="5 mm [THT]"]
  LED7 = LED - 5mm [color="Yellow (592nm)" package="5 mm [THT]"]
  LED8 = LED - 5mm [color="Yellow (592nm)" package="5 mm [THT]"]
  LED9 = LED - 5mm [color="Yellow (592nm)" package="5 mm [THT]"]
  LED10 = LED - 5mm [color="Yellow (592nm)" package="5 mm [THT]"]
  LED11 = LED - 5mm [color="Blue (470nm)" package="5 mm [THT]"]
  R1 = Resistor [tolerance=±5% resistance=220 package=THT]
  R2 = Resistor [tolerance=±5% resistance=220 package=THT]
  R3 = Resistor [tolerance=±5% resistance=220 package=THT]
  R4 = Resistor [tolerance=±5% resistance=220 package=THT]
  R5 = Resistor [tolerance=±5% resistance=220 package=THT]
  R6 = Resistor [tolerance=±5% resistance=220 package=THT]
  R7 = Resistor [tolerance=±5% resistance=220 package=THT]
  R8 = Resistor [tolerance=±5% resistance=220 package=THT]
  R9 = Resistor [tolerance=±5% resistance=220 package=THT]
  R10 = Resistor [tolerance=±5% resistance=220 package=THT]
  R11 = Resistor [tolerance=±5% resistance=220 package=THT]

nets:
  N1: Bauteil1.D8, LED5.anode
  N2: Bauteil1.D9_PWM, LED10.anode
  N3: Bauteil1.D10_PWM/SS, LED9.anode
  N4: Bauteil1.D11_PWM/MOSI, LED8.anode
  N5: Bauteil1.D12/MISO, LED7.anode
  N6: Bauteil1.D13/SCK, LED6.anode
  N7: Bauteil1.GND, R1.Pin_1, R2.Pin_1, R3.Pin_1, R4.Pin_1, R5.Pin_1, R6.Pin_1, R7.Pin_1, R8.Pin_1, R9.Pin_1, R10.Pin_1, R11.Pin_1
  N8: Bauteil1.D2, LED11.anode
  N9: Bauteil1.D4, LED1.anode
  N10: Bauteil1.D5_PWM, LED3.anode
  N11: Bauteil1.D6_PWM, LED2.anode
  N12: Bauteil1.D7, LED4.anode
  N13: LED1.cathode, R3.Pin_0
  N14: LED2.cathode, R5.Pin_0
  N15: LED3.cathode, R4.Pin_0
  N16: LED4.cathode, R7.Pin_0
  N17: LED5.cathode, R10.Pin_0
  N18: LED6.cathode, R1.Pin_0
  N19: LED7.cathode, R2.Pin_0
  N20: LED8.cathode, R6.Pin_0
  N21: LED9.cathode, R11.Pin_0
  N22: LED10.cathode, R8.Pin_0
  N23: LED11.cathode, R9.Pin_0
