# Fritzing sketch id868_Act_2_0 (saved by Fritzing 0.9.3b)
breadboards: 1

parts:
  U1 = 7-SEGMENT-DISPLAY [package=7-segment-display]
  S3 = Momentary Switch [package=tactile_switch_smd]
  S2 = Momentary Switch [package=tactile_switch_smd]
  R1 = Resistor [tolerance=±5% resistance=10k package="1206 [SMD]"]
  R2 = Resistor [tolerance=±5% resistance=10k package="1206 [SMD]"]
  R3 = Resistor [tolerance=±5% resistance=10k package="1206 [SMD]"]
  R4 = Resistor [tolerance=±5% resistance=10k package="1206 [SMD]"]
  S4 = Momentary Switch [package=tactile_switch_smd]
  Part1 = Arduino Uno (Rev3)
  S1 = Momentary Switch [package=tactile_switch_smd]
  R5 = Resistor [tolerance=±5% resistance=10k package="1206 [SMD]"]
  R6 = Resistor [tolerance=±5% resistance=10k package="1206 [SMD]"]

nets:
  N1: U1.E, Part1.D8
  N2: U1.D, Part1.D6_PWM
  N3: U1.G1, R6.Pin_0
  N4: U1.C, Part1.D5_PWM
  N5: U1.B, Part1.D2
  N6: U1.A, Part1.D1/TX
  N7: U1.G2, R5.Pin_0
  N8: U1.F, Part1.D3_PWM
  N9: U1.G, Part1.D4
  N10: S3.1, R3.Pin_0, Part1.D10_PWM/SS
  N11: S3.3, S2.3, S4.3, Part1.5V, S1.3, R5.Pin_1
  N12: S2.1, R2.Pin_0, Part1.D11_PWM/MOSI
  N13: R1.Pin_0, Part1.D12/MISO, S1.1
  N14: R1.Pin_1, R2.Pin_1, R3.Pin_1, R4.Pin_1, Part1.GND, R6.Pin_1
  N15: R4.Pin_0, S4.1, Part1.D9_PWM
