# Fritzing sketch id869_Bionic_Hand_Wiring_0 (saved by Fritzing 0.9.3b)
breadboards: 1

parts:
  J1 = Basic Servo
  J3 = Basic Servo
  J4 = Basic Force Sensing Resistor (FSR) [package=THT]
  J5 = Basic Force Sensing Resistor (FSR) [package=THT]
  J6 = Basic Force Sensing Resistor (FSR) [package=THT]
  J7 = Basic Force Sensing Resistor (FSR) [package=THT]
  J8 = Basic Force Sensing Resistor (FSR) [package=THT]
  VCC1 = 4 x AAA Battery Mount
  R2 = Resistor [tolerance=±5% resistance=220 package=THT]
  R3 = Resistor [tolerance=±5% resistance=220 package=THT]
  R5 = Resistor [tolerance=±5% resistance=220 package=THT]
  R6 = Resistor [tolerance=±5% resistance=220 package=THT]
  R8 = Resistor [tolerance=±5% resistance=220 package=THT]
  J2 = Basic Servo
  Part1 = Arduino Uno (Rev3)
  VCC2 = Battery block 9V  # not connected

nets:
  GND: J1.gnd, J3.gnd, VCC1.-, R2.Pin_0, R3.Pin_0, R5.Pin_0, R6.Pin_0, R8.Pin_0, J2.gnd, Part1.GND
  VCC: J1.vcc, J3.vcc, VCC1.+, J2.vcc
  N1: J1.pulse, Part1.D4
  N2: J3.pulse, Part1.D3_PWM
  N3: J4.pin_0, J5.pin_0, J6.pin_0, J7.pin_0, J8.pin_0, Part1.5V
  N4: J4.pin_1, R6.Pin_1, Part1.A0
  N5: J5.pin_1, R2.Pin_1, Part1.A1
  N6: J6.pin_1, R3.Pin_1, Part1.A4/SDA
  N7: J7.pin_1, R5.Pin_1, Part1.A2
  N8: J8.pin_1, R8.Pin_1, Part1.A3
  N9: J2.pulse, Part1.D2
