# Fritzing sketch id86_2MotorShield_0 (saved by Fritzing 0.9.2b)
circuit board: 6.14142cm x 5.35707cm
breadboards: 1

parts:
  J2 = female pin header, 4 pins [form="♀ (female)"]
  Onderdeel1 = EasyDriver_v44
  Onderdeel2 = EasyDriver_v44
  J3 = female pin header, 4 pins [form="♀ (female)"]
  J4 = female pin header, 2 pins [form="♀ (female)"]
  J5 = female pin header, 2 pins [form="♀ (female)"]
  J1 = Screw terminal - 2 pins [package=THT]

nets:
  N1: J2.pin1, Onderdeel2.OUT1B
  N2: J2.pin2, Onderdeel2.OUT1A
  N3: J2.pin3, Onderdeel2.OUT2B
  N4: J2.pin4, Onderdeel2.OUT2A
  GND: Onderdeel1.GND, Onderdeel2.GND, J1.pin1
  N5: Onderdeel1.V+, Onderdeel2.V+, J1.pin2
  N6: Onderdeel1.STEP, J4.pin2
  N7: Onderdeel1.DIR, J4.pin1
  N8: Onderdeel1.OUT2A, J3.pin4
  N9: Onderdeel1.OUT2B, J3.pin3
  N10: Onderdeel1.OUT1A, J3.pin2
  N11: Onderdeel1.OUT1B, J3.pin1
  N12: Onderdeel2.STEP, J5.pin2
  N13: Onderdeel2.DIR, J5.pin1
