# Fritzing sketch id870_Birduino_0 (saved by Fritzing 0.7.12b)
breadboards: 1

parts:
  Arduino1 = Arduino  # not connected
  Part1 = Triple Axis Accelerometer Breakout - ADXL335
  Arduino_Ethernet_Shield1 = Arduino Ethernet Shield  # not connected
  LED1 = LED - 5mm [color="Red (633nm)" package="5 mm [THT]"]  # not connected
  Arduino2 = Arduino
  U1 = microSD Socket [package="Molex 502774-0891 [SMD]"]  # not connected

nets:
  N1: Part1.YOUT, Arduino2.A1
  N2: Part1.XOUT, Arduino2.A0
  GND: Part1.GND, Arduino2.GND

notes:
  SD Card
