# Fritzing sketch id873_Switch_0 (saved by Fritzing 0.9.1b)

parts:
  Part1 = Arduino Uno (Rev3)
  S1 = SPST Switch [package=switche-dpdt]
  Q1 = Basic FET N-Channel [package="D2Pak [SMD]"]

nets:
  N1: Part1.D13/SCK, Q1.drain
  N2: Part1.GND, S1.P, Q1.Gate
  N3: Part1.D2, S1.S
