# Fritzing sketch id874_Printentflechtung_Fertig_NEw_0 (saved by Fritzing 0.9.2b)
circuit board: 6.88566cm x 5.36311cm

parts:
  R1 = Resistor [tolerance=±5% resistance=330 package=THT]
  R3 = Resistor [tolerance=±5% resistance=10k package=THT]
  Poti = TRIMPOT [package=trimpot_pth_s3_lock]
  SD-Karte = MicroSD Card Module
  Höhen-Sensor = Altitude/Pressure Sensor - MPL3115A2 Breakout [part_number=SEN-11084]
  Neigungs-Sensor = SparkFun RPI-1031 Tilt-a-Whirl Breakout [part_number=SEN-10621]
  Taster = Header 2 [package=molex-1x2_lock]
  R2 = Resistor [tolerance=±5% resistance=330 package=THT]
  GPS-Modul = Header 3 [package=molex-1x3_lock]
  Display = M16 [package=1x16_machine-pin-header_lock.004]
  R4 = Resistor [tolerance=±5% resistance=330 package=THT]
  J&J_Production = Arduino Uno (Rev3)

nets:
  N1: R1.Pin_0, J&J_Production.A4/SDA
  N2: R1.Pin_1, Höhen-Sensor.SDA
  GND: R3.Pin_0, Poti.CCW, SD-Karte.GND, Höhen-Sensor.GND, Neigungs-Sensor.GND, GPS-Modul.1, Display.1, Display.5, Display.16, J&J_Production.GND
  N3: R3.Pin_1, Taster.2, J&J_Production.A2
  N4: Poti.WIPER, Display.3
  VCC: Poti.CW, SD-Karte.VCC, Neigungs-Sensor.VCC, Taster.1, Display.2, R4.Pin_0, J&J_Production.5V
  N5: SD-Karte.MISO, J&J_Production.D12/MISO
  N6: SD-Karte.MOSI, J&J_Production.D11_PWM/MOSI
  N7: SD-Karte.SCK, J&J_Production.D13/SCK
  N8: SD-Karte.CS, J&J_Production.D10_PWM/SS
  N9: Höhen-Sensor.SCL, R2.Pin_1
  VCC_2: Höhen-Sensor.VCC, GPS-Modul.2, J&J_Production.3V3
  N10: Neigungs-Sensor.S1, J&J_Production.D3_PWM
  N11: Neigungs-Sensor.S2, J&J_Production.D2
  N12: R2.Pin_0, J&J_Production.A5/SCL
  N13: GPS-Modul.3, J&J_Production.D9_PWM
  N14: Display.4, J&J_Production.A1
  N15: Display.6, J&J_Production.A0
  N16: Display.11, J&J_Production.D7
  N17: Display.12, J&J_Production.D6_PWM
  N18: Display.13, J&J_Production.D5_PWM
  N19: Display.14, J&J_Production.D4
  N20: Display.15, R4.Pin_1
