# Fritzing sketch id875_Blaulicht__0 (saved by Fritzing 0.9.3b)
breadboards: 1

parts:
  Bauteil1 = Arduino Uno (Rev3)
  LED1 = LED - 5mm [color="Blue (525nm)" package="5 mm [THT]"]
  LED2 = LED - 5mm [color="Blue (525nm)" package="5 mm [THT]"]
  R1 = Resistor [tolerance=±5% resistance=220 package=THT]
  R2 = Resistor [tolerance=±5% resistance=220 package=THT]

nets:
  N1: Bauteil1.D12/MISO, R2.Pin_0
  N2: Bauteil1.D13/SCK, R1.Pin_0
  N3: Bauteil1.GND, LED1.cathode, LED2.cathode
  N4: LED1.anode, R2.Pin_1
  N5: LED2.anode, R1.Pin_1
