# Fritzing sketch id876_Switch_0 (saved by Fritzing 0.9.3b)
breadboards: 1

parts:
  S2 = Reed switch [package=THT]
  R2 = Resistor [tolerance=±5% resistance=10k package=THT]
  Componente2 = makenai0000
  LED2 = LED - 5mm [color="Red (633nm)" package="5 mm [THT]"]

nets:
  N1: S2.pin_1, R2.Pin_0, Componente2.connector4, Componente2.connector9
  N2: R2.Pin_1, Componente2.connector35, LED2.cathode
  N3: Componente2.connector19, LED2.anode

notes:
  reed switch
  10K ohm resistor
  led
