# Fritzing sketch id877_3_0 (saved by Fritzing 0.9.2b)
breadboards: 1

parts:
  パーツ2 = Arduino Uno (Rev3)
  J1 = Piezo Speaker
  U2 = LM4871 [package=so08]
  R1 = Resistor [tolerance=±5% resistance=3.3k package=THT]
  R2 = Resistor [tolerance=±5% resistance=1.5k package=THT]
  C1 = Ceramic Capacitor [capacitance=100nF package="100 mil [THT, multilayer]"]
  R3 = Resistor [tolerance=±5% resistance=3.3k package=THT]
  R4 = Resistor [tolerance=±5% resistance=1.5k package=THT]
  R5 = Resistor [tolerance=±5% resistance=3.3k package=THT]
  R6 = Resistor [tolerance=±5% resistance=1.5k package=THT]
  U5 = microSD Socket [package=usd-socket-pp]
  パーツ4 = blueIOT core

nets (from the schematic view):
  N1: パーツ2.D9_PWM, U2.IN+, U2.IN-
  3V3: パーツ2.D11_PWM/MOSI, パーツ2.3V3, パーツ2.5V, J1.pin1, U2.BYPASS, U2.VDD, U2.V02, R1.Pin_0, R2.Pin_0, C1.1, R4.Pin_1, U5.VCC, パーツ4.P21
  N2: パーツ2.D13/SCK, R6.Pin_1
  N3: パーツ2.D0/RX, パーツ4.D10
  N4: パーツ2.D1/TX, パーツ4.MOSI
  GND: パーツ2.D4, パーツ2.GND, U2.SHUTDWN, U2.GND, R1.Pin_1, R3.Pin_0, R3.Pin_1
  N5: J1.pin2, U2.V01
  N6: R2.Pin_1, R5.Pin_0, U5.DI
  N7: C1.0, R4.Pin_0, U5.DO, パーツ4.P22
  N8: パーツ4.SCK, パーツ4.MISO
