# Fritzing sketch id878_Blim_Blim_0 (saved by Fritzing 0.9.3b)
breadboards: 1

parts:
  R2 = Resistor [tolerance=±5% resistance=220 package=THT]
  R3 = Resistor [tolerance=±5% resistance=220 package=THT]
  R4 = Resistor [tolerance=±5% resistance=220 package=THT]
  LED1 = RGB LED (com. anode, rbg) [package="5 mm [THT]"]
  Componente1 = Arduino Uno (Rev3)

nets:
  N1: R2.Pin_0, LED1.blue_cathode
  N2: R2.Pin_1, Componente1.D10_PWM/SS
  N3: R3.Pin_0, LED1.green_cathode
  N4: R3.Pin_1, Componente1.D9_PWM
  N5: R4.Pin_0, LED1.red_cathode
  N6: R4.Pin_1, Componente1.D11_PWM/MOSI
  N7: LED1.common_anode, Componente1.GND

notes:
  Blim Blim
  Hello my name is Angel I am a beginner but this code I did (maybe that's why it's very simple) so if you put it into practice Thank you
  In this project a 3-color Led (red, green and blue) is used.
  The code is very simple.
  The Breadboard is something smaller for aesthetics but there is no problem if a normal one is used.
  Blim Blim
  Hola me llamo Angel soy un principiante pero este codigo lo hice yo (tal vez por eso es muy simple) asi que si lo pones en practica Muchas Gracias
  En este proyecto se usa un Led de 3 colores (rojo, verde y azul).
  El codigo muy simple.
  El Breadboard es algo mas pequeño por estetica pero no hay proble si se usa una normal.
