# Fritzing sketch id87_2trct50002leds2Motoressamyhuerta_0 (saved by Fritzing 0.9.3b)
breadboards: 1

parts:
  S1 = Ponte-H L298N
  Componente1 = Arduino Uno (Rev3)
  M1 = DC Motor
  M2 = DC Motor
  LED1 = LED - 5mm [color="Red (633nm)" package="5 mm [THT]"]
  LED2 = LED - 5mm [color="Red (633nm)" package="5 mm [THT]"]
  R2 = 10k
  R7 = Resistor [tolerance=±5% resistance=10 package="0402 [SMD]"]
  R8 = Resistor [tolerance=±5% resistance=10 package="0402 [SMD]"]
  R9 = 10k
  R10 = 10k
  R1 = 10k

nets:
  N1: S1.connector1, R7.Pin_0, R1.connector0
  N2: S1.connector5, Componente1.D11_PWM/MOSI
  N3: S1.connector6, Componente1.D10_PWM/SS
  N4: S1.connector7, Componente1.D9_PWM
  N5: S1.connector8, Componente1.D8
  N6: S1.connector10, M2.pin_2
  N7: S1.connector11, M2.pin_1
  N8: S1.connector13, M1.pin_2
  N9: S1.connector14, M1.pin_1
  N10: Componente1.A0, R8.Pin_0
  N11: Componente1.A1, R7.Pin_1
  N12: Componente1.D2, LED2.anode
  N13: Componente1.D3_PWM, LED1.anode
  N14: Componente1.5V, R2.connector1
  N15: Componente1.GND, R9.connector1
  N16: LED1.cathode, R10.connector1
  N17: LED2.cathode, R9.connector0
