# Fritzing sketch id882_Blink_Fritzing_0 (saved by Fritzing 0.7.12b)
breadboards: 1

parts:
  Arduino1 = Arduino
  LED1 = LED - 5mm [color="Red (633nm)" package="5 mm [THT]"]
  R1 = Resistor [tolerance=±5% resistance=220 package=THT]

nets:
  N1: Arduino1.D13, LED1.cathode
  N2: Arduino1.GND, R1.Pin_1
  N3: LED1.anode, R1.Pin_0

notes:
  Mr. Swifts Blink Fritzing Projcect]
