# Fritzing sketch id884_drawing_0 (saved by Fritzing 0.9.2b)
breadboards: 1

parts:
  Part1 = Arduino Uno (Rev3)
  R1 = Resistor [tolerance=±5% resistance=4.7k package="2010 [SMD]"]
  R2 = Resistor [tolerance=±5% resistance=100k package="2010 [SMD]"]
  RGB_SMD_LED1 = SMD RGB LED (WS2812) [package=5050]

nets:
  N1: Part1.D6_PWM, R1.Pin_1
  5V: Part1.5V, RGB_SMD_LED1.VDD
  GND: Part1.GND, R2.Pin_1, RGB_SMD_LED1.VSS
  N2: R1.Pin_0, R2.Pin_0, RGB_SMD_LED1.DIn
