# Fritzing sketch id885_blinker_0 (saved by Fritzing 0.7.11b)
breadboards: 1

parts:
  LED1 = LED - 5mm [color="Red (633nm)" package="5 mm [THT]"]
  LED2 = LED - 5mm [color="Red (633nm)" package="5 mm [THT]"]
  LED3 = LED - 5mm [color="Red (633nm)" package="5 mm [THT]"]
  LED4 = LED - 5mm [color="Red (633nm)" package="5 mm [THT]"]
  R1 = Resistor [tolerance=±5% resistance=220 package=THT]
  R2 = Resistor [tolerance=±5% resistance=220 package=THT]
  R3 = Resistor [tolerance=±5% resistance=220 package=THT]
  Arduino1 = Arduino
  R4 = Resistor [tolerance=±5% resistance=220 package=THT]

nets:
  N1: LED1.cathode, R1.Pin_1
  N2: LED1.anode, Arduino1.D7
  N3: LED2.cathode, R4.Pin_1
  N4: LED2.anode, Arduino1.D6
  N5: LED3.cathode, R2.Pin_0
  N6: LED3.anode, Arduino1.D5
  N7: LED4.cathode, R3.Pin_0
  N8: LED4.anode, Arduino1.D4
  N9: R1.Pin_0, R2.Pin_1, R3.Pin_1, Arduino1.GND, R4.Pin_0
