# Fritzing sketch id886_blinkingled_0 (saved by Fritzing 0.9.2b)
breadboards: 1

parts:
  U1 = 555 Timer [package="DIP8 [THT]"]
  C1 = Electrolytic Capacitor [capacitance=1µF package="100 mil [THT, electrolytic]"]
  LED1 = LED - 5mm [color="Red (633nm)" package="5 mm [THT]"]
  R1 = Resistor [tolerance=±5% resistance=330 package=THT]
  R2 = Resistor [tolerance=±5% resistance=560 package=THT]

nets:
  N1: U1.Ground, C1.-, LED1.cathode
  N2: U1.Trigger, U1.Threshold, C1.+, R1.Pin_1
  N3: U1.Output, LED1.anode
  N4: U1.Reset, U1.Vcc_Supply_Voltage, R2.Pin_0
  N5: U1.Discharge, R1.Pin_0, R2.Pin_1
