# Fritzing sketch id887_Mosfet_LCD_0 (saved by Fritzing 0.9.0b)
circuit board: 8.46667cm x 5.64444cm
breadboards: 1

parts:
  Componente1 = Arduino Uno (Rev3)
  S1 = Pushbutton [package="[THT]"]
  S2 = Pushbutton [package="[THT]"]
  R1 = Resistor [tolerance=±5% resistance=470 package=THT]
  R2 = Resistor [tolerance=±5% resistance=470 package=THT]
  LCD1 = LCD screen
  LED1 = LED - 5mm [color="Red (633nm)" package="5 mm [THT]"]
  LED2 = LED - 5mm [color="Green (555nm)" package="5 mm [THT]"]
  LED3 = LED - 5mm [color="Yellow (595nm)" package="5 mm [THT]"]
  Q1 = NPN-Transistor [package="TO92 [THT]"]
  R3 = Resistor [tolerance=±5% resistance=470 package=THT]
  R4 = Resistor [tolerance=±5% resistance=4.7k package=THT]
  R5 = Resistor [tolerance=±5% resistance=4.7k package=THT]

nets:
  N1: Componente1.D8, S2.Pin_1, S2.Pin_2, LED2.cathode
  N2: Componente1.D9_PWM, S1.Pin_1, S1.Pin_2, LED1.cathode
  N3: Componente1.D11_PWM/MOSI, LCD1.E
  N4: Componente1.D12/MISO, LCD1.RS
  GND: Componente1.GND, R1.Pin_1, R2.Pin_1, LCD1.VSS, LCD1.R/W, Q1.E, R4.Pin_1, R5.Pin_0
  N5: Componente1.D2, LCD1.DB7
  N6: Componente1.D3_PWM, LCD1.DB6
  N7: Componente1.D4, LCD1.DB5
  N8: Componente1.D5_PWM, LCD1.DB4
  N9: Componente1.D6_PWM, Q1.B
  N10: Componente1.D7, R3.Pin_0
  5V: Componente1.5V, S1.Pin_3, S1.Pin_4, S2.Pin_3, S2.Pin_4, LCD1.VDD, LCD1.LED+
  N11: R1.Pin_0, LED2.anode
  N12: R2.Pin_0, LED1.anode
  N13: LCD1.V0, R4.Pin_0
  N14: LCD1.LED-, R5.Pin_1
  N15: LED3.cathode, Q1.C
  N16: LED3.anode, R3.Pin_1
