# Fritzing sketch id888_ledtomusic_0 (saved by Fritzing 0.9.2b)
breadboards: 1

parts:
  rgb_led_strip = RGB LED - (4 legs) [package="5 mm [THT]"]
  Part1 = Arduino Uno (Rev3)
  Q1 = Basic FET N-Channel [package="D2Pak [SMD]"]
  Q2 = Basic FET N-Channel [package="D2Pak [SMD]"]
  Q3 = Basic FET N-Channel [package="D2Pak [SMD]"]
  R1 = Resistor [tolerance=±5% resistance=10k package=THT]
  R2 = Resistor [tolerance=±5% resistance=10k package=THT]
  R3 = Resistor [tolerance=±5% resistance=10k package=THT]
  IC1 = MSGEQ7 [package=soic8]
  C1 = Ceramic Capacitor [capacitance=100nF package="100 mil [THT, multilayer]"]
  C2 = Ceramic Capacitor [capacitance=33pF package="100 mil [THT, multilayer]"]
  C3 = Ceramic Capacitor [capacitance=100nF package="100 mil [THT, multilayer]"]
  C4 = Ceramic Capacitor [capacitance=10nF package="100 mil [THT, multilayer]"]
  R4 = Resistor [tolerance=±5% resistance=220 package=THT]
  TRS1 = Audio Jack (TRS) 3.5mm [package="PG203J [THT]"]

nets:
  N1: rgb_led_strip.red_cathode, Q3.drain, R3.Pin_0
  N2: rgb_led_strip.common_anode, Q2.drain, R2.Pin_0
  N3: rgb_led_strip.green_cathode, Q1.drain, R1.Pin_0
  N4: rgb_led_strip.blue_cathode, Part1.VIN
  N5: Part1.A0, IC1.DCOUT
  N6: Part1.D9_PWM, Q3.Gate
  N7: Part1.D10_PWM/SS, Q2.Gate
  N8: Part1.D11_PWM/MOSI, Q1.Gate
  GND: Part1.GND, Q1.source, Q2.source, Q3.source, R1.Pin_1, R2.Pin_1, R3.Pin_1, IC1.GND, C1.1, C2.0, C3.1, TRS1.Sleeve
  N9: Part1.D2, IC1.STROBE
  N10: Part1.D4, IC1.RESET
  5V: Part1.5V, IC1.VDD, C1.0, R4.Pin_0
  N11: IC1.AUDIO_IN, C4.0
  N12: IC1.CG, C3.0
  N13: IC1.CKIN, C2.1, R4.Pin_1
  N14: C4.1, TRS1.Ring

notes:
  220k
  resistor
  C1 C2
  C3
  C4
  C1: 33pF
  C2: 100nF
  C3: 10nF
  C4: 100nF
  10k resistors
  make sure to plug the correct colored wire into the correct port on your led strip
  3.5 mm audio in goes here
  \/ \/ \/
