# Fritzing sketch id890_uno_music_leds_0 (saved by Fritzing 0.9.2b)
circuit board: 8.53413cm x 4.61426cm
circuit board: 2.96045cm x 3.25782cm
circuit board: 2.03071cm x 1.81934cm
breadboards: 1

parts:
  rgb_led_strip = RGB LED - (4 legs) [part_number="RGB LED strip 5050" package="5 mm [THT]"]
  Arduino = Arduino Uno (Rev3)
  Q1 = Basic FET N-Channel [part_number="RFP50N06 50N06 POWER MOSFET N-CHANNEL 60V 50A" package="D2Pak [SMD]"]
  Q2 = Basic FET N-Channel [part_number="RFP50N06 50N06 POWER MOSFET N-CHANNEL 60V 50A" package="D2Pak [SMD]"]
  Q3 = Basic FET N-Channel [part_number="RFP50N06 50N06 POWER MOSFET N-CHANNEL 60V 50A" package="D2Pak [SMD]"]
  R2 = Resistor [tolerance=±5% resistance=10k package=THT]
  R3 = Resistor [tolerance=±5% resistance=10k package=THT]
  C4 = Ceramic Capacitor [capacitance=100nF voltage=6.3V package="100 mil [THT, multilayer]"]
  C1 = Ceramic Capacitor [capacitance=33pF package="100 mil [THT, multilayer]"]
  C2 = Ceramic Capacitor [capacitance=100nF package="100 mil [THT, multilayer]"]
  C3 = Ceramic Capacitor [capacitance=10nF package="100 mil [THT, multilayer]"]
  TRS1 = Audio Jack (TRS) 3.5mm [package="PG203J [THT]"]
  R1 = Resistor [tolerance=±5% resistance=10k package=THT]
  MSGEQ7 = IC, DIP package, 8 pins [chip_label=MSGEQ7]
  R4 = Resistor [tolerance=±5% resistance=220k package=THT]

nets:
  N1: rgb_led_strip.red_cathode, Q1.drain, R1.Pin_0
  N2: rgb_led_strip.common_anode, Q2.drain, R2.Pin_0
  N3: rgb_led_strip.green_cathode, Q3.drain, R3.Pin_0
  N4: rgb_led_strip.blue_cathode, Arduino.VIN
  N5: Arduino.A0, MSGEQ7.pin3
  N6: Arduino.D9_PWM, Q3.Gate
  N7: Arduino.D10_PWM/SS, Q2.Gate
  N8: Arduino.D11_PWM/MOSI, Q1.Gate
  N9: Arduino.GND, Q1.source, Q2.source, Q3.source, R2.Pin_1, R3.Pin_1, C4.1, C1.0, C2.1, TRS1.Sleeve, R1.Pin_1, MSGEQ7.pin2
  N10: Arduino.D2, MSGEQ7.pin4
  N11: Arduino.D4, MSGEQ7.pin7
  N12: Arduino.5V, C4.0, MSGEQ7.pin1, R4.Pin_0
  N13: C1.1, MSGEQ7.pin8, R4.Pin_1
  N14: C2.0, MSGEQ7.pin6
  N15: C3.0, MSGEQ7.pin5
  N16: C3.1, TRS1.Ring

notes:
  R4 220k
  resistor
  C1 C2
  C3
  C4
  C1: 33pF
  C2: 100nF
  C3: 10nF
  C4: 100nF
  R1-R3 10k resistors
  LED strip
  audio in
  DC 12V, 5A
