# Fritzing sketch id891_WeeBlinky_0 (saved by Fritzing 0.9.0b)
breadboards: 1

parts:
  R1 = Resistor [tolerance=±5% resistance=1k package=THT]
  R2 = Resistor [tolerance=±5% resistance=1k package=THT]
  R3 = Resistor [tolerance=±5% resistance=33k package=THT]
  R4 = Resistor [tolerance=±5% resistance=33k package=THT]
  C1 = Electrolytic Capacitor [capacitance=10µF package="100 mil [THT, electrolytic]"]
  C2 = Electrolytic Capacitor [capacitance=10µF package="100 mil [THT, electrolytic]"]
  LED1 = LED - 5mm [color="Red (633nm)" package="5 mm [THT]"]
  LED2 = LED - 5mm [color="Red (633nm)" package="5 mm [THT]"]
  Q1 = NPN-Transistor [package="TO92 [THT]"]
  Q2 = NPN-Transistor [package="TO92 [THT]"]

nets:
  N1: R1.Pin_0, R2.Pin_0, C1.+, C2.+, Q1.C, Q2.C
  N2: R1.Pin_1, LED1.cathode
  N3: R2.Pin_1, LED2.cathode
  N4: R3.Pin_0, R4.Pin_0, C1.-, C2.-, Q1.B, Q2.B
  4.5V: R3.Pin_1, R4.Pin_1, LED1.anode, LED2.anode
  GND: Q1.E, Q2.E
