# Fritzing sketch id894_Blow_sensor_with_ATtiny85_0 (saved by Fritzing 0.9.0b)
breadboards: 1

parts:
  LED1 = smd LED [color="Red (633nm)" package="0805 [SMD]"]
  LED2 = smd LED [color="Red (633nm)" package="0805 [SMD]"]
  LED3 = smd LED [color="Red (633nm)" package="0805 [SMD]"]
  LED4 = smd LED [color="Red (633nm)" package="0805 [SMD]"]
  R1 = Resistor [tolerance=±5% resistance=220 package=THT]
  U1 = MIC [package=mic_electret_smd]
  U2 = attiny85 [package=dip]
  BAT2 = Battery Holders [package=battcon_12mm]
  S1 = Round Pushbutton

nets:
  N1: LED1.cathode, LED2.cathode, LED3.cathode, LED4.cathode, R1.Pin_0, U1.2, U2.Pin_4, BAT2.-, S1.leg0
  N2: LED1.anode, U2.Pin_2
  N3: LED2.anode, U2.Pin_7
  N4: LED3.anode, U2.Pin_6
  N5: LED4.anode, U2.Pin_5
  N6: R1.Pin_1, U2.Pin_8, BAT2.+
  N7: U1.1, U2.Pin_3
  N8: U2.Pin_1, S1.leg1

notes:
  R1 = 10K
  Battery 3V (CR2032)
  Microcontroller ATtiny85
  This Schema and the Source Code
  From http://simonetti.media.mit.edu/~jieqi/2012/01/electret-microphone-example-code/
