# Fritzing sketch id895_bluetooth+temperature_extension_0 (saved by Fritzing 0.8.3b)
circuit board: 6.88561cm x 5.36311cm
breadboards: 1

parts:
  Bluetooth = female pin header, 2 pins [form="♀ (female)"]
  J2 = female pin header, 2 pins [form="♀ (female)"]
  Temperature = LM34 Temperature Sensor [package="TO92 [THT]"]
  Servo = Basic Servo
  Servo_2 = Basic Servo
  Part1 = Arduino Uno (Rev3)

nets:
  VCC: Bluetooth.pin1, Temperature.+Vs, Servo.vcc, Servo_2.vcc, Part1.5V
  GND: Bluetooth.pin2, Temperature.GND, Servo.gnd, Servo_2.gnd, Part1.GND
  N1: J2.pin1, Part1.D2
  N2: J2.pin2, Part1.D3_PWM
  N3: Temperature.Vout, Part1.A0
  N4: Servo.pulse, Part1.ICSP_SCK, Part1.D13/SCK
  N5: Servo_2.pulse, Part1.D12/MISO

notes:
  iliusvla
  rev 0.1
