# Fritzing sketch id896_led_strip_mosfet_0 (saved by Fritzing 0.9.1b)
circuit board: 8.46667cm x 5.64444cm
breadboards: 1

parts:
  U1 = attiny85 [package=dip]
  Q1 = Basic FET N-Channel [package="TO220 [THT]"]
  R1 = Resistor [tolerance=±5% resistance=220 package=THT]
  R2 = Resistor [tolerance=±5% resistance=220 package=THT]
  R3 = Resistor [tolerance=±5% resistance=220 package=THT]
  LED2 = RGB LED (com. anode, rbg) [package="5 mm [THT]"]
  Power_plug1 = Power plug
  Part1 = Arduino Uno (Rev3)
  Part2 = Bluetooth Mate Silver
  Q4 = Basic FET N-Channel [package="TO220 [THT]"]
  Q5 = Basic FET N-Channel [package="TO220 [THT]"]

nets:
  N1: U1.Pin_4, Q1.source, Power_plug1.GND, Q4.source, Q5.source
  N2: U1.Pin_5, R1.Pin_0
  N3: U1.Pin_6, R2.Pin_0
  N4: U1.Pin_7, R3.Pin_0
  N5: U1.Pin_8, Part1.D13/SCK
  N6: Q1.gate, R1.Pin_1
  N7: Q1.drain, LED2.blue_cathode
  N8: R2.Pin_1, Q4.gate
  N9: R3.Pin_1, Q5.gate
  N10: LED2.red_cathode, Q4.drain
  N11: LED2.common_anode, Power_plug1.VCC
  N12: LED2.green_cathode, Q5.drain
  GND: Part1.GND, Part2.GND
  N13: Part1.D0/RX, Part2.TX_5V
  N14: Part1.D1/TX, Part2.RX_5V
  5V: Part1.5V, Part2.VCC

notes:
  volt 12 volts for led strip
  a led concept as 12 volts leds strip
