# Fritzing sketch id897_Untitled_Sketch_0 (saved by Fritzing 0.9.3b)
breadboards: 1

parts:
  Εξάρτημα1 = Arduino Uno (Rev3)
  IC1 = L293D [package=THT]
  Εξάρτημα2 = Bluetooth HC-05 Macho
  VCC1 = Battery block 9V
  M1 = DC Motor
  M2 = DC Motor

nets:
  N1: Εξάρτημα1.D11_PWM/MOSI, IC1.In_3, M1.pin_1
  N2: Εξάρτημα1.D12/MISO, IC1.Out_4_(_Controlled_by_Enable_2_)
  GND: Εξάρτημα1.GND, IC1.0V, Εξάρτημα2.GND, VCC1.-, VCC1.+
  N3: Εξάρτημα1.D0/RX, Εξάρτημα2.TXD
  N4: Εξάρτημα1.D1/TX, Εξάρτημα2.RXD
  N5: Εξάρτημα1.D2, IC1.In_1
  N6: Εξάρτημα1.D4, IC1.In_2
  5V: Εξάρτημα1.5V, IC1.Enable_1, IC1.+Vmotor, IC1.Enable_2, IC1.+V, Εξάρτημα2.VCC
  N7: IC1.Out_1_(_Controlled_by_Enable_1_), M2.pin_1
  N8: IC1.Out_2_(_Controlled_by_Enable_1_), M2.pin_2
  N9: IC1.In_4, M1.pin_2

notes:
  Δεξιός κινητήρας
  Αριστερός κινητήρας
