# Fritzing sketch id898_Untitled_Sketch_2_0 (saved by Fritzing 0.9.2b)
breadboards: 1

parts:
  S1 = Pushbutton [package="[THT]"]
  S2 = Pushbutton [package="[THT]"]
  Part3 = Arduino BT
  S3 = Pushbutton [package="[THT]"]
  R1 = Resistor [tolerance=±5% resistance=10 package=THT]
  R2 = Resistor [tolerance=±5% resistance=10 package=THT]
  R3 = Resistor [tolerance=±5% resistance=10 package=THT]
  LED1 = RGB LED (com. anode, rbg) [package="5 mm [THT]"]
  R4 = Resistor [tolerance=±5% resistance=220 package=THT]
  R5 = Resistor [tolerance=±5% resistance=220 package=THT]
  R6 = Resistor [tolerance=±5% resistance=220 package=THT]

nets:
  N1: S1.Pin_1, S1.Pin_2, Part3.PWM_D5, R1.Pin_0
  N2: S1.Pin_3, S1.Pin_4, S2.Pin_3, S2.Pin_4, Part3.GND, S3.Pin_3, S3.Pin_4, LED1.common_anode
  N3: S2.Pin_1, S2.Pin_2, Part3.PWM_D6, R2.Pin_0
  N4: Part3.MOSI/PWM_D11, R5.Pin_1
  N5: Part3.MISO/D12, R6.Pin_1
  N6: Part3.SCK/D13, R4.Pin_1
  N7: Part3.RESET_WT11/D7, S3.Pin_1, S3.Pin_2, R3.Pin_0
  N8: Part3.5V, R1.Pin_1, R3.Pin_1
  N9: LED1.red_cathode, R4.Pin_0
  N10: LED1.blue_cathode, R6.Pin_0
  N11: LED1.green_cathode, R5.Pin_0
