# Fritzing sketch id8_Untitled_Sketch_0 (saved by Fritzing 0.7.10b)
breadboards: 1

parts:
  Arduino2 = Arduino
  LED1 = LED - 5mm [color="Red (633nm)" package="5 mm [THT]"]
  R1 = Resistor [tolerance=±5% resistance=510 package=THT]

nets:
  N1: Arduino2.GND, LED1.cathode
  N2: Arduino2.D10, R1.Pin_0
  N3: LED1.anode, R1.Pin_1
