# Fritzing sketch id900_GarageDoor_0 (saved by Fritzing 0.9.3b)
breadboards: 1

parts:
  LED1 = LED - 5mm [color="Green (565nm)" package="5 mm [THT]"]
  U1 = atmega328 [package=dip]  # not connected
  R1 = Resistor [tolerance=±5% resistance=220 package=THT]
  C1 = Ceramic Capacitor [capacitance=10pF voltage=10V package="100 mil [THT, multilayer]"]
  Part1 = Bluetooth HC-05 Macho
  KY-1 = keyes

nets:
  N1: LED1.cathode, C1.1, Part1.GND, KY-1.connector2
  N2: LED1.anode, R1.Pin_0
  N3: R1.Pin_1, C1.0, Part1.VCC, KY-1.connector1
