# Fritzing sketch id901_hc_05_0 (saved by Fritzing 0.9.1b)

parts:
  JY-MCU = Arduino Nano (Rev3.0)
  Part1 = Bluetooth HC-05 Macho

nets:
  N1: JY-MCU.D10, Part1.TXD
  N2: JY-MCU.D11/MOSI, Part1.RXD
  GND: JY-MCU.GND, Part1.GND
  5V: JY-MCU.5V, Part1.VCC
