# Fritzing sketch id903_Arduino_Bluetoothdimmer_0 (saved by Fritzing 0.9.3b)
breadboards: 1

parts:
  Bauteil1 = Arduino Uno (Rev3)
  Bauteil2 = Bluetooth HC-05 Macho  # not connected
  R1 = Resistor [tolerance=±5% resistance=220 package=THT]
  LED1 = smd LED [color="Red (633nm)" package="0805 [SMD]"]

nets:
  N1: Bauteil1.D9_PWM, LED1.cathode
  N2: Bauteil1.GND, R1.Pin_0
  N3: R1.Pin_1, LED1.anode
