# Fritzing sketch id904_Arduino_Bluetoothdimmer_b14xawk_0 (saved by Fritzing 0.9.3b)
breadboards: 1

parts:
  Bauteil1 = Arduino Uno (Rev3)
  Bluetooth_HC-05 = Bluetooth HC-05 Macho
  R1 = Resistor [tolerance=±5% resistance=220 package=THT]
  LED1 = smd LED [color="Red (633nm)" package="0805 [SMD]"]

nets:
  N1: Bauteil1.D9_PWM, LED1.cathode
  N2: Bauteil1.D10_PWM/SS, Bluetooth_HC-05.RXD
  N3: Bauteil1.D11_PWM/MOSI, Bluetooth_HC-05.TXD
  GND: Bauteil1.GND, Bluetooth_HC-05.GND, R1.Pin_0
  5V: Bauteil1.5V, Bluetooth_HC-05.VCC
  N4: R1.Pin_1, LED1.anode
