# Fritzing sketch id907_final_project_ledsbluetooth_0 (saved by Fritzing 0.9.1b)
circuit board: 8.46667cm x 5.64444cm
breadboards: 2

parts:
  Q1 = Basic FET N-Channel [package="TO220 [THT]"]
  Q2 = Basic FET P-Channel [package="DPak [SMD]"]
  R1 = Resistor [tolerance=±5% resistance=220 package=THT]
  R2 = Resistor [tolerance=±5% resistance=220 package=THT]
  Q3 = Basic FET P-Channel [package="DPak [SMD]"]
  R3 = Resistor [tolerance=±5% resistance=220 package=THT]
  LED2 = RGB LED (com. anode, rbg) [package="5 mm [THT]"]
  Power_plug1 = Power plug
  Part2 = Bluetooth Mate Silver
  U2 = Voltage Regulator - 5V [package="TO220 [THT]"]
  U3 = atmega168 [package=dip]
  XTAL1 = Crystal [frequency="16 Mhz" package=THT]
  R4 = Resistor [tolerance=±5% resistance=2.2k package=THT]
  R5 = Resistor [tolerance=±5% resistance=1k package=THT]
  C3 = Ceramic Capacitor [capacitance=22pF package="100 mil [THT, multilayer]"]
  C4 = Ceramic Capacitor [capacitance=100nF package="100 mil [THT, multilayer]"]

nets:
  N1: Q1.gate, R1.Pin_1
  N2: Q1.drain, LED2.blue_cathode
  GND: Q1.source, Q2.source, Q3.source, Power_plug1.GND, Part2.GND, U2.GND, U3.GND, R4.Pin_0, C3.0, C4.1
  N3: Q2.Gate, R2.Pin_1
  N4: Q2.drain, LED2.red_cathode
  N5: R1.Pin_0, U3.D3_(PWM)
  N6: R2.Pin_0, U3.D5_(PWM)
  N7: Q3.Gate, R3.Pin_1
  N8: Q3.drain, LED2.green_cathode
  N9: R3.Pin_0, U3.D6_(PWM)
  N10: LED2.common_anode, Power_plug1.VCC, U2.input_voltage
  N11: Part2.RX_5V, R5.Pin_0
  N12: Part2.TX_5V, U3.D0_(RX)
  VCC: Part2.VCC, U2.output_voltage, U3.VCC, U3.AVCC
  N13: U3.D1_(TX), R4.Pin_1, R5.Pin_1
  N14: U3.XLAT1, XTAL1.pin_1, C4.0
  N15: U3.XLAT2, XTAL1.pin_0, C3.1

notes:
  12 volts output leds strip
  a led concept as 12 volts leds strip
  voltage regular to 5, not 12 volts !
