# Fritzing sketch id908_Bluetooth_0 (saved by Fritzing 0.9.2b)
breadboards: 1

parts:
  Part1 = Arduino Uno (Rev3)
  Part2 = HC-06
  LED1 = LED - 5mm [color="Green (555nm)" package="5 mm [THT]"]
  LED2 = LED - 5mm [color="Red (633nm)" package="5 mm [THT]"]
  R1 = Resistor [tolerance=±5% resistance=100 package="0603 [SMD]"]
  R2 = Resistor [tolerance=±5% resistance=100 package="0603 [SMD]"]
  R3 = PHOTOCELL [package=photocell-kit]
  R4 = Resistor [tolerance=±5% resistance=220 package="1206 [SMD]"]

nets:
  N1: Part1.A0, R3.P$1, R4.Pin_0
  N2: Part1.D8, LED1.anode
  N3: Part1.D9_PWM, LED2.anode
  N4: Part1.D0/RX, Part2.connector13
  N5: Part1.D1/TX, Part2.connector12
  N6: Part1.5V, Part2.connector15, R3.P$2
  N7: Part1.GND, Part2.connector14, R1.Pin_1, R2.Pin_1, R4.Pin_1
  N8: LED1.cathode, R2.Pin_0
  N9: LED2.cathode, R1.Pin_0
