# Fritzing sketch id909_carwledsandbluetooth_0 (saved by Fritzing 0.9.0b)
breadboards: 1

parts:
  Part1 = Arduino Uno (Rev3)
  IC1 = H-Bridge [package=THT]
  VCC1 = Battery
  VCC2 = Battery
  LED1 = LED - 5mm [color="Red (633nm)" package="5 mm [THT]"]
  LED2 = LED - 5mm [color="Yellow (595nm)" package="5 mm [THT]"]
  LED3 = smd LED [color="Orange (620nm)" package="0805 [SMD]"]
  LED3_2 = smd LED [color="Orange (620nm)" package="1206 [SMD]"]
  LED4 = LED - 5mm [color="Green (565nm)" package="5 mm [THT]"]
  M1 = DC Motor
  M2 = DC Motor
  Part2 = Bluetooth Mate Silver
  U1 = SWITCH_SPDT [package=kps-1290]

nets:
  N1: Part1.D8, IC1.2A
  N2: Part1.D10_PWM/SS, Part2.VCC
  N3: Part1.D11_PWM/MOSI, Part2.CTS_5V
  N4: Part1.D12/MISO, IC1.3A
  N5: Part1.D13/SCK, IC1.4A
  N6: Part1.D2, LED4.anode
  N7: Part1.D3_PWM, LED3.anode, LED3_2.anode
  N8: Part1.D4, LED2.anode
  N9: Part1.D5_PWM, LED1.anode
  N10: Part1.D7, IC1.1A
  N11: Part1.5V, IC1.1_2EN, IC1.VCC2, IC1.3_4EN, IC1.VCC1, VCC1.+, VCC2.+, Part2.RX_5V
  GND: Part1.GND, IC1.GND1, IC1.GND2, IC1.GND3, IC1.GND4, LED1.cathode, LED2.cathode, LED3.cathode, LED3_2.cathode, LED4.cathode, Part2.TX_5V, U1.O
  N12: IC1.1Y, M1.pin_2
  N13: IC1.2Y, M1.pin_1
  N14: IC1.3Y, M2.pin_2
  N15: IC1.4Y, M2.pin_1
  N16: VCC1.-, VCC2.-
