# Fritzing sketch id910_BTSerial_0 (saved by Fritzing 0.9.2b)

parts:
  부품1 = Arduino Uno (Rev3)
  부품2 = HC-06

nets:
  N1: 부품1.D2, 부품2.connector13
  N2: 부품1.D3_PWM, 부품2.connector12
  N3: 부품1.5V, 부품2.connector15
  N4: 부품1.GND, 부품2.connector14
