# Fritzing sketch id911_2tempEEPCB_0 (saved by Fritzing 0.9.0b)
circuit board: 2.31314cm x 1.82108cm
breadboards: 1

parts:
  DS18 = SO08 [chip_label=IC package=SO]
  24L = EEPROM-I2C [package=so08]
  R2 = Resistor [tolerance=±5% resistance=4.7k part_number=1 package="0805 [SMD]"]
  T1 = TMP36 Temperature Sensor [package="TO92 [THT]"]

nets:
  N1: DS18.3, R2.Pin_0, T1.Vout
  N2: DS18.4, R2.Pin_1, T1.+Vs
  VSS: DS18.5, 24L.A0, 24L.A1, 24L.A2, 24L.VSS, 24L.WP, T1.GND
