# Fritzing sketch id912_bluetoothLight_0 (saved by Fritzing 0.9.3b)
circuit board: 5.95923cm x 6.3306cm
breadboards: 1

parts:
  HC-06 = Bluetooth HC-05 Macho
  Arduino_UNO = Arduino Uno (Rev3)
  Relay_5V = keyes
  S1 = Pushbutton [package="[THT]"]
  R1 = Resistor [tolerance=±5% resistance=10k package=THT]

nets:
  N1: HC-06.TXD, Arduino_UNO.D0/RX
  N2: HC-06.RXD, Arduino_UNO.D1/TX
  VCC: HC-06.VCC, Arduino_UNO.5V, Relay_5V.connector1, S1.Pin_3, S1.Pin_4
  GND: HC-06.GND, Arduino_UNO.GND, Relay_5V.connector2, R1.Pin_0
  N3: Arduino_UNO.D12/MISO, S1.Pin_1, S1.Pin_2, R1.Pin_1
  N4: Arduino_UNO.D13/SCK, Relay_5V.connector0
  N5: Relay_5V.connector3, Relay_5V.connector4, Relay_5V.connector5
