# Fritzing sketch id915_BlynkDoorLock_0 (saved by Fritzing 0.9.2b)

parts:
  KY-4 = keyes
  부품1 = Arduino Yun

nets:
  N1: KY-4.connector0, 부품1.D2/SDA, 부품1.D2
  N2: KY-4.connector1, 부품1.5V
  N3: KY-4.connector2, 부품1.GND

notes:
  Electric Door stirike
  12V GND
  12V VCC
