# Fritzing sketch id916_CheckSensorValue_0 (saved by Fritzing 0.9.2b)
breadboards: 1

parts:
  U1 = POT [package=pot_mammoth]
  부품1 = Arduino Yun

nets:
  N1: U1.S, 부품1.GND
  N2: U1.A, 부품1.A0
  N3: U1.E, 부품1.5V
