# Fritzing sketch id918_HumanCounter_0 (saved by Fritzing 0.9.2b)
breadboards: 1

parts:
  부품1 = Arduino Yun
  LED1 = LED - 5mm [color="Red (633nm)" package="5 mm [THT]"]
  R1 = Resistor [tolerance=±5% resistance=220 package=THT]
  PIR1 = PIR_sensor

nets:
  N1: 부품1.5V, PIR1.connector1
  N2: 부품1.D13/SCK, LED1.anode
  N3: 부품1.GND, R1.Pin_0, PIR1.connector3
  N4: 부품1.D2, PIR1.connector2
  N5: LED1.cathode, R1.Pin_1
