# Fritzing sketch id91_74hc595_project_6d_0 (saved by Fritzing 0.9.3b)
circuit board: 4.8cm x 4.6cm
breadboards: 1

parts:
  74hc595 = 74HC595 [package="DIP16 [THT]"]
  74hc595_2 = 74HC595 [package="DIP16 [THT]"]
  R16 = Resistor [tolerance=±5% resistance=220 package=THT]
  R15 = Resistor [tolerance=±5% resistance=220 package=THT]
  R14 = Resistor [tolerance=±5% resistance=220 package=THT]
  R13 = Resistor [tolerance=±5% resistance=220 package=THT]
  R12 = Resistor [tolerance=±5% resistance=220 package=THT]
  R11 = Resistor [tolerance=±5% resistance=220 package=THT]
  R10 = Resistor [tolerance=±5% resistance=220 package=THT]
  R9 = Resistor [tolerance=±5% resistance=220 package=THT]
  R8 = Resistor [tolerance=±5% resistance=220 package=THT]
  R7 = Resistor [tolerance=±5% resistance=220 package=THT]
  R6 = Resistor [tolerance=±5% resistance=220 package=THT]
  R5 = Resistor [tolerance=±5% resistance=220 package=THT]
  R4 = Resistor [tolerance=±5% resistance=220 package=THT]
  R3 = Resistor [tolerance=±5% resistance=220 package=THT]
  R2 = Resistor [tolerance=±5% resistance=220 package=THT]
  R1 = Resistor [tolerance=±5% resistance=220 package=THT]
  JP1 = Header 6 [package=molex-1x6_lock]
  1 = smd LED [color="Red (633nm)" package="0805 [SMD]"]
  2 = smd LED [color="Red (633nm)" package="0805 [SMD]"]
  3 = smd LED [color="Red (633nm)" package="0805 [SMD]"]
  4 = smd LED [color="Red (633nm)" package="0805 [SMD]"]
  5 = smd LED [color="Red (633nm)" package="0805 [SMD]"]
  6 = smd LED [color="Red (633nm)" package="0805 [SMD]"]
  7 = smd LED [color="Red (633nm)" package="0805 [SMD]"]
  8 = smd LED [color="Red (633nm)" package="0805 [SMD]"]
  9 = smd LED [color="Red (633nm)" package="0805 [SMD]"]
  10 = smd LED [color="Red (633nm)" package="0805 [SMD]"]
  11 = smd LED [color="Red (633nm)" package="0805 [SMD]"]
  12 = smd LED [color="Red (633nm)" package="0805 [SMD]"]
  13 = smd LED [color="Red (633nm)" package="0805 [SMD]"]
  14 = smd LED [color="Red (633nm)" package="0805 [SMD]"]
  15 = smd LED [color="Red (633nm)" package="0805 [SMD]"]
  16 = smd LED [color="Red (633nm)" package="0805 [SMD]"]

nets:
  N1: 74hc595.Q1, 7.anode
  N2: 74hc595.Q2, 6.anode
  N3: 74hc595.Q3, 5.anode
  N4: 74hc595.Q4, 4.anode
  N5: 74hc595.Q5, 3.anode
  N6: 74hc595.Q6, 2.anode
  N7: 74hc595.Q7, 1.anode
  GND: 74hc595.GND, 74hc595.OE, 74hc595_2.GND, 74hc595_2.OE, R16.Pin_0, R15.Pin_0, R14.Pin_0, R13.Pin_0, R12.Pin_0, R11.Pin_0, R10.Pin_0, R9.Pin_0, R8.Pin_0, R7.Pin_0, R6.Pin_0, R5.Pin_0, R4.Pin_0, R3.Pin_0, R2.Pin_0, R1.Pin_0, JP1.1
  N8: 74hc595.Q7', 74hc595_2.DS
  VCC: 74hc595.MR, 74hc595.VCC, 74hc595_2.MR, 74hc595_2.VCC, JP1.2
  N9: 74hc595.SH_CP, 74hc595_2.SH_CP, JP1.4
  N10: 74hc595.ST_CP, 74hc595_2.ST_CP, JP1.3
  N11: 74hc595.DS, JP1.5
  N12: 74hc595.Q0, 8.anode
  N13: 74hc595_2.Q1, 15.anode
  N14: 74hc595_2.Q2, 14.anode
  N15: 74hc595_2.Q3, 13.anode
  N16: 74hc595_2.Q4, 12.anode
  N17: 74hc595_2.Q5, 11.anode
  N18: 74hc595_2.Q6, 10.anode
  N19: 74hc595_2.Q7, 9.anode
  N20: 74hc595_2.Q7', JP1.6
  N21: 74hc595_2.Q0, 16.anode
  N22: R16.Pin_1, 16.cathode
  N23: R15.Pin_1, 15.cathode
  N24: R14.Pin_1, 14.cathode
  N25: R13.Pin_1, 13.cathode
  N26: R12.Pin_1, 12.cathode
  N27: R11.Pin_1, 11.cathode
  N28: R10.Pin_1, 10.cathode
  N29: R9.Pin_1, 9.cathode
  N30: R8.Pin_1, 8.cathode
  N31: R7.Pin_1, 7.cathode
  N32: R6.Pin_1, 6.cathode
  N33: R5.Pin_1, 5.cathode
  N34: R4.Pin_1, 4.cathode
  N35: R3.Pin_1, 3.cathode
  N36: R2.Pin_1, 2.cathode
  N37: R1.Pin_1, 1.cathode

notes:
  74hc595 (C) Rene Wennekes
  GND VCC LATCH CLK DIN DOUT
