# Fritzing sketch id920_BlynkCandyHand_0 (saved by Fritzing 0.9.3b)
breadboards: 1

parts:
  Part1 = SparkFun ESP8266 Thing
  VCC1 = 4 x AAA Battery Mount
  J1 = Basic Servo
  J2 = Basic Servo

nets:
  GND: Part1.GND, VCC1.-, J1.gnd, J2.gnd
  N1: Part1.GPIO16, J2.pulse
  N2: Part1.GPIO15, J1.pulse
  N3: VCC1.+, J2.vcc

notes:
  ESP8266 is powered by USB power. It should not be connected to 6v. servo power.
  I used the Sparkfun Blynk board. The Thing will work also. Just connect GPIO 15 & 16 to servo control lines.
