# Fritzing sketch id921_Arduino_BMA280_0 (saved by Fritzing 0.9.0b)
breadboards: 1

parts:
  Bauteil2 = Arduino Uno (Rev3)
  R1 = Resistor [tolerance=±5% resistance=4.7k package=THT]
  R2 = Resistor [tolerance=±5% resistance=4.7k package=THT]
  Bauteil1 = prefix0000

nets:
  N1: Bauteil2.A4/SDA, R1.Pin_1, Bauteil1.connector9
  N2: Bauteil2.A5/SCL, R2.Pin_0, Bauteil1.connector19
  N3: Bauteil2.GND, Bauteil1.connector8, Bauteil1.connector15, Bauteil1.connector16
  N4: Bauteil2.3V3, R1.Pin_0, R2.Pin_1, Bauteil1.connector10, Bauteil1.connector14
