# Fritzing sketch id924_BMP180_LSD1602A_0 (saved by Fritzing 0.9.2b)
circuit board: 8.46667cm x 5.64444cm
breadboards: 1

parts:
  Часть1 = Arduino Uno (Rev3)
  LCD1 = LCD screen
  R1 = Trimmer Potentiometer [maximum_resistance=10kΩ package=THT]
  BMP180_(GY-68) = BMP180

nets:
  N1: Часть1.A4/SDA, BMP180_(GY-68).connector10
  N2: Часть1.A5/SCL, BMP180_(GY-68).connector9
  N3: Часть1.D10_PWM/SS, LCD1.E
  N4: Часть1.D11_PWM/MOSI, LCD1.RS
  N5: Часть1.D2, LCD1.DB7
  N6: Часть1.D3_PWM, LCD1.DB6
  N7: Часть1.D4, LCD1.DB5
  N8: Часть1.D5_PWM, LCD1.DB4
  N9: Часть1.3V3, BMP180_(GY-68).connector5
  5V: Часть1.5V, LCD1.VDD, LCD1.R/W, LCD1.LED+, R1.leg2
  GND: Часть1.GND, LCD1.VSS, LCD1.LED-, R1.leg1, BMP180_(GY-68).connector6
  N10: LCD1.V0, R1.wiper
