# Fritzing sketch id925_Hastighed_og_alarm_lamper_BMW_0 (saved by Fritzing 0.9.3b)
breadboards: 1

parts:
  D1 = Rectifier Diode [part_number=1N4001 package="300 mil [THT]"]
  D2 = Rectifier Diode [part_number=1N4001 package="300 mil [THT]"]
  D3 = Rectifier Diode [part_number=1N4001 package="300 mil [THT]"]
  D4 = Rectifier Diode [part_number=1N4001 package="300 mil [THT]"]
  R1 = Resistor [tolerance=±5% resistance=100 package=THT]
  J1 = Camdenboss CTB0158-4 [part_number=CTB0158-4 package=THT]
  J2 = Camdenboss CTB0158-4 [part_number=CTB0158-4 package=THT]
  LED1 = LED - 5mm [color="Yellow (592nm)" package="5 mm [THT]"]
  LED2 = LED - 5mm [color="Blue (505nm)" package="5 mm [THT]"]
  R3 = Resistor [tolerance=±5% resistance=220 package=THT]
  LED3 = LED - 5mm [color="Red (633nm)" package="5 mm [THT]"]
  U1 = LM393 [package=so08]
  R4 = Resistor [tolerance=±5% resistance=4.7k package=THT]
  C1 = Electrolytic Capacitor [capacitance=4.7µF voltage=35V package="100 mil [THT, electrolytic]"]
  R5 = Resistor [tolerance=±5% resistance=10k package=THT]
  R6 = Resistor [tolerance=±5% resistance=10k package=THT]
  R7 = Resistor [tolerance=±5% resistance=10k package=THT]
  Q1 = NPN-Transistor [package="TO92 [THT]"]
  R8 = Resistor [tolerance=±5% resistance=10k package=THT]

nets:
  N1: D1.cathode, D4.anode, LED1.cathode
  N2: D1.anode, D2.anode, D3.anode, J2.pin4
  N3: D2.cathode, J1.pin2, LED2.cathode
  N4: D3.cathode, J1.pin1, LED3.cathode
  N5: D4.cathode, R1.Pin_1, J1.pin3
  N6: R1.Pin_0, J1.pin4, R3.Pin_1, U1.G1_V+, R8.Pin_1
  N7: J2.pin1, Q1.C, R8.Pin_0
  N8: J2.pin2, R4.Pin_0
  N9: J2.pin3, U1.G1_V-, C1.-, R5.Pin_1, R7.Pin_1, Q1.E
  N10: LED1.anode, LED2.anode, R3.Pin_0, LED3.anode
  N11: U1.G1_OUT, R6.Pin_0
  N12: U1.G1_-IN, R5.Pin_0
  N13: U1.G1_+IN, R4.Pin_1, C1.+
  N14: R6.Pin_1, R7.Pin_0, Q1.B

notes:
  Grøn/Sort
  Lyseblå
  Lilla/Sort
  Brun/Grøn
  Blå
  Brun
  Gul
  Hvid
