# Fritzing sketch id928_Kotel1_0 (saved by Fritzing 0.9.3b)
circuit board: 8.46667cm x 5.64444cm

parts:
  Часть1 = Arduino Mega 2560 (Rev3)
  Часть2 = Arduino Ethernet Shield (Rev3)
  M2 = Dagu DGServo 9g (Top view) [part_number=RS001B]
  M3 = Dagu DGServo 9g (Top view) [part_number=RS001B]
  GLCD_128x1 = 128 x 64 Graphic LCD
  DS3 = DS18B20 1-Wire Temperature Sensor [part_number=DS18B20]
  DS4 = DS18B20 1-Wire Temperature Sensor [part_number=DS18B20]
  DS1 = DS18B20 1-Wire Temperature Sensor [part_number=DS18B20]
  DS2 = DS18B20 1-Wire Temperature Sensor [part_number=DS18B20]
  R1 = Resistor [tolerance=±5% resistance=220 package=THT]
  R2 = Resistor [tolerance=±5% resistance=220 package=THT]
  R3 = Resistor [tolerance=±5% resistance=220 package=THT]
  R4 = Resistor [tolerance=±5% resistance=220 package=THT]
  THERMO1 = MAX31855_Breakout_Board_with_Thermocouple
  U2 = LM3480IM4 [package=sot23-3]
  Power_plug1 = Power plug
  M4 = Dagu DGServo 9g (Top view) [part_number=RS001B]
  U3 = Relay8

nets:
  5V: Часть1.5V, DS1.VDD, R4.Pin_0, THERMO1.connector1
  N1: Часть1.D28, THERMO1.connector4
  N2: Часть1.D44, GLCD_128x1.4_D/I
  N3: Часть1.D45, U3.connector4
  N4: Часть1.D46, GLCD_128x1.5_R/W
  N5: Часть1.D47, U3.connector0
  N6: Часть1.D48, GLCD_128x1.6_Enable
  N7: Часть1.D49, U3.connector13
  N8: Часть1.D51, U3.connector14
  N9: Часть1.D53, U3.connector21, U3.connector31
  GND: Часть1.GND, DS1.GND
  N10: Часть2.PWM_D11, M4.pulse
  N11: Часть2.SPI/D12, M2.pulse
  N12: Часть2.SPI/D13, M3.pulse
  GND_2: Часть2.GND, M3.gnd, U2.IN, Power_plug1.GND
  N13: Часть2.VIN, U2.OUT
  VCC: M3.vcc, Power_plug1.VCC, M4.vcc
  N14: GLCD_128x1.15_CS1, GLCD_128x1.18_Vout
  N15: DS3.DQ, R2.Pin_1
  N16: DS3.VDD, R2.Pin_0
  N17: DS4.DQ, R3.Pin_1
  N18: DS1.DQ, R4.Pin_1
  N19: DS2.DQ, R1.Pin_1
  N20: U2.GND, U3.connector11
