# Fritzing sketch id92_CNC_Grbl_0 (saved by Fritzing 0.9.3b)
breadboards: 2

parts:
  Part1 = Arduino Uno (Rev3)
  X_Controller = EasyDriver_v44
  Y_Controller = EasyDriver_v44
  Z_Controller = EasyDriver_v44
  X_Axis = Stepper Motor - Bipolar
  Y_Axis = Stepper Motor - Bipolar
  Z_Axis = Stepper Motor - Bipolar
  12v_Vin = Power plug
  Limit_X = Round Pushbutton
  Endstop_X = Round Pushbutton
  Limit_Y = Round Pushbutton
  Endstop_Y = Round Pushbutton
  Limit_Z = Round Pushbutton
  Endstop_Z = Round Pushbutton
  R1 = Resistor [tolerance=±5% resistance=10k package="2512 [SMD]"]
  R2 = Resistor [tolerance=±5% resistance=10k package="2512 [SMD]"]
  R3 = Resistor [tolerance=±5% resistance=10k package="2512 [SMD]"]
  R4 = Resistor [tolerance=±5% resistance=10k package="2512 [SMD]"]
  R5 = Resistor [tolerance=±5% resistance=10k package="2512 [SMD]"]
  R6 = Resistor [tolerance=±5% resistance=10k package="2512 [SMD]"]
  Reset = Round Pushbutton
  R7 = Resistor [tolerance=±5% resistance=10k package="2512 [SMD]"]
  Feed_Hold = Round Pushbutton
  Cycle_Start/Resume = Round Pushbutton
  R8 = Resistor [tolerance=±5% resistance=10k package="2512 [SMD]"]
  R9 = Resistor [tolerance=±5% resistance=10k package="2512 [SMD]"]

nets:
  N1: Part1.A0, R7.Pin_0
  N2: Part1.A1, R8.Pin_0
  N3: Part1.A2, R9.Pin_0
  N4: Part1.D8, X_Controller.ENABLE, Y_Controller.ENABLE, Z_Controller.ENABLE
  N5: Part1.D9_PWM, R1.Pin_0, R2.Pin_0
  N6: Part1.D10_PWM/SS, R3.Pin_0, R4.Pin_0
  N7: Part1.D12/MISO, R5.Pin_0, R6.Pin_0
  N8: Part1.D2, X_Controller.STEP
  N9: Part1.D3_PWM, Y_Controller.STEP
  N10: Part1.D4, Z_Controller.STEP
  N11: Part1.D5_PWM, X_Controller.DIR
  N12: Part1.D6_PWM, Y_Controller.DIR
  N13: Part1.D7, Z_Controller.DIR
  VCC: Part1.5V, X_Controller.VCC, Y_Controller.VCC, Z_Controller.VCC, Feed_Hold.leg0, Cycle_Start/Resume.leg0
  GND: Part1.GND, X_Controller.GND, Y_Controller.GND, Z_Controller.GND, 12v_Vin.GND, Limit_X.leg0, Endstop_X.leg0, Limit_Y.leg0, Endstop_Y.leg0, Limit_Z.leg0, Endstop_Z.leg0, Reset.leg0
  N14: X_Controller.V+, Y_Controller.V+, Z_Controller.V+, 12v_Vin.VCC
  N15: X_Controller.OUT2A, X_Axis.A
  N16: X_Controller.OUT2B, X_Axis.C
  N17: X_Controller.OUT1A, X_Axis.B
  N18: X_Controller.OUT1B, X_Axis.D
  N19: Y_Controller.OUT2A, Y_Axis.A
  N20: Y_Controller.OUT2B, Y_Axis.C
  N21: Y_Controller.OUT1A, Y_Axis.B
  N22: Y_Controller.OUT1B, Y_Axis.D
  N23: Z_Controller.OUT2A, Z_Axis.A
  N24: Z_Controller.OUT2B, Z_Axis.C
  N25: Z_Controller.OUT1A, Z_Axis.B
  N26: Z_Controller.OUT1B, Z_Axis.D
  N27: Limit_X.leg1, R1.Pin_1
  N28: Endstop_X.leg1, R2.Pin_1
  N29: Limit_Y.leg1, R3.Pin_1
  N30: Endstop_Y.leg1, R4.Pin_1
  N31: Limit_Z.leg1, R5.Pin_1
  N32: Endstop_Z.leg1, R6.Pin_1
  N33: Reset.leg1, R7.Pin_1
  N34: Feed_Hold.leg1, R8.Pin_1
  N35: Cycle_Start/Resume.leg1, R9.Pin_1
