# Fritzing sketch id930_bootloader_0 (saved by Fritzing 0.9.0b)
breadboards: 1

parts:
  DRV2 = usbmini
  DRV3 = usbmini
  U1 = atmega328 [package=dip]
  R1 = Resistor [tolerance=±5% resistance=1k package=THT]
  R2 = Resistor [tolerance=±5% resistance=1k package=THT]
  R3 = Resistor [tolerance=±5% resistance=1k package=THT]
  LED2 = LED - 3mm [color="Green (555nm)" package="3 mm [THT]"]
  LED1 = LED - 3mm [color="Red (633nm)" package="3 mm [THT]"]
  LED3 = LED - 3mm [color="Yellow (585nm)" package="3 mm [THT]"]
  U2 = atmega328 [package=dip]
  C1 = Ceramic Capacitor [capacitance=100nF voltage=6.3V package="100 mil [THT, multilayer]"]
  C2 = Ceramic Capacitor [capacitance=100nF package="100 mil [THT, multilayer]"]
  R4 = Resistor [tolerance=±5% resistance=1k package=THT]
  LED4 = LED - 3mm [color="Blue (430nm)" package="3 mm [THT]"]
  R5 = Resistor [tolerance=±5% resistance=10k package=THT]
  R6 = Resistor [tolerance=±5% resistance=10k package=THT]

nets:
  GND: DRV2.connector130, DRV3.connector130, U1.GND, LED2.cathode, LED1.cathode, LED3.cathode, U2.GND, LED4.cathode
  N1: DRV2.connector131, U1.D0_(RX)
  N2: DRV2.connector132, U1.D1_(TX)
  VCC: DRV2.connector133, DRV3.connector133, U1.VCC, U1.AVCC, U2.VCC, U2.AVCC, R4.Pin_0, R5.Pin_1, R6.Pin_1
  N3: DRV2.connector143, C1.0
  N4: DRV3.connector131, U2.D0_(RX)
  N5: DRV3.connector132, U2.D1_(TX)
  N6: DRV3.connector143, C2.0
  N7: U1.RESET, C1.1, R5.Pin_0
  N8: U1.D3_(PWM), U2.XLAT1
  N9: U1.D6_(PWM), R3.Pin_1
  N10: U1.D7, R2.Pin_1
  N11: U1.D8, R1.Pin_1
  N12: U1.D10_(PWM), U2.RESET, C2.1, R6.Pin_0
  N13: U1.D11_(PWM), U2.D11_(PWM)
  N14: U1.D12, U2.D12
  N15: U1.D13, U2.D13
  N16: R1.Pin_0, LED1.anode
  N17: R2.Pin_0, LED2.anode
  N18: R3.Pin_0, LED3.anode
  N19: R4.Pin_1, LED4.anode
