# Fritzing sketch id931_bot_alarma_0 (saved by Fritzing 0.9.3b)
breadboards: 1

parts:
  Componente1 = Arduino Uno (Rev3)  # not connected
  R1 = Resistor [tolerance=±5% resistance=220 package=THT]
  J1 = Piezo Speaker  # not connected
  LED1 = LED - 5mm [color="Red (633nm)" package="5 mm [THT]"]
  R2 = Resistor [tolerance=±5% resistance=220 package=THT]
  LED2 = LED - 5mm [color="Red (633nm)" package="5 mm [THT]"]

nets:
  N1: R1.Pin_0, R2.Pin_0
  N2: R1.Pin_1, LED1.cathode
  N3: R2.Pin_1, LED2.cathode
