# Fritzing sketch id932_tarea_kprada_0 (saved by Fritzing 0.9.3b)
breadboards: 1

parts:
  Parte3 = HC-SR04 ultrasonic distance sensor
  Componente1 = Arduino Uno (Rev3)
  R1 = Resistor [tolerance=±5% resistance=220 package=THT]
  R2 = Resistor [tolerance=±5% resistance=220 package=THT]
  LED1 = LED - 5mm [color="Red (633nm)" package="5 mm [THT]"]
  LED2 = LED - 5mm [color="Red (633nm)" package="5 mm [THT]"]
  J1 = Piezo Speaker

nets:
  N1: Parte3.connector0, Componente1.5V
  N2: Parte3.connector1, Componente1.D10_PWM/SS
  N3: Parte3.connector2, Componente1.D11_PWM/MOSI
  N4: Parte3.connector3, Componente1.GND, R1.Pin_1, R2.Pin_1, J1.pin1
  N5: Componente1.D8, J1.pin2
  N6: Componente1.D3_PWM, LED1.anode
  N7: Componente1.D4, LED2.anode
  N8: R1.Pin_0, LED2.cathode
  N9: R2.Pin_0, LED1.cathode

notes:
  [aqui coloca la resistencia
  GND es negativo
