# Fritzing sketch id933_bot_alarma_of_0 (saved by Fritzing 0.9.3b)
breadboards: 1

parts:
  LED1 = LED - 5mm [color="Red (633nm)" package="5 mm [THT]"]
  LED2 = LED - 5mm [color="Red (633nm)" package="5 mm [THT]"]
  J1 = Piezo Speaker
  Componente1 = Arduino Uno (Rev3)
  R1 = Resistor [tolerance=±5% resistance=220 package=THT]
  R2 = Resistor [tolerance=±5% resistance=220 package=THT]
  Parte3 = HC-SR04 ultrasonic distance sensor

nets:
  N1: LED1.cathode, R1.Pin_0
  N2: LED1.anode, Componente1.D3_PWM
  N3: LED2.cathode, R2.Pin_0
  N4: LED2.anode, Componente1.D4
  N5: J1.pin1, Componente1.GND, R1.Pin_1, R2.Pin_1, Parte3.connector3
  N6: J1.pin2, Componente1.D5_PWM
  N7: Componente1.D10_PWM/SS, Parte3.connector2
  N8: Componente1.D11_PWM/MOSI, Parte3.connector1
  N9: Componente1.5V, Parte3.connector0
