# Fritzing sketch id934_Boton_Debounce_y_motor_FFH_0 (saved by Fritzing 0.9.2b)
circuit board: 6.88566cm x 5.36311cm
breadboards: 1

parts:
  S1 = Pushbutton [package=THT]
  R1 = Resistor [tolerance=±5% resistance=10k package=THT]
  Arduino1 = Arduino Uno (Rev3)
  LED1 = LED - 5mm [color="Red (633nm)" package="5 mm [THT]"]
  Q1 = NPN-Transistor [package="TO92 [THT]"]
  R2 = Resistor [tolerance=±5% resistance=220 package=THT]
  M1 = DC Motor

nets:
  N1: S1.leg0, R1.Pin_0, Arduino1.D2
  N2: S1.leg1, Arduino1.5V
  N3: R1.Pin_1, Arduino1.GND, LED1.cathode, M1.pin_2
  N4: Arduino1.D9_PWM, R2.Pin_1
  N5: Arduino1.D13/SCK, LED1.anode
  N6: Arduino1.3V3, Q1.E
  N7: Q1.B, R2.Pin_0
  N8: Q1.C, M1.pin_1

notes:
  In this example, a pushbutton is used as a digital input and an LED is a digital output.
  Related example: http://arduino.cc/en/Tutorial/Button
