# Fritzing sketch id935_darth_vader_star_war_nano_0 (saved by Fritzing 0.9.2b)
breadboards: 1

parts:
  J1 = Piezo Speaker
  R1 = Resistor [tolerance=±5% resistance=220 package=THT]
  LED2 = LED - 5mm [color="Red (633nm)" package="5 mm [THT]"]
  Parte1 = Arduino Nano (Rev3.0)
  LED3 = LED - 5mm [color="Red (633nm)" package="5 mm [THT]"]
  R2 = Resistor [tolerance=±5% resistance=220 package=THT]

nets:
  N1: J1.pin1, LED2.cathode, Parte1.D2, LED3.cathode, R2.Pin_1
  N2: J1.pin2, Parte1.D9
  N3: R1.Pin_0, Parte1.D4
  N4: R1.Pin_1, LED2.anode, LED3.anode
  N5: Parte1.D6, R2.Pin_0

notes:
  Proyecto Darth Vader Star War Music
  Arduino Nano
