# Fritzing sketch id936_MyBQv6_0 (saved by Fritzing 0.7.9b)
breadboards: 1

parts:
  IC1 = SMD_QFN-16 [chip_label=IC part_number=BQ25504RGT]
  Chvr = Ceramic Capacitor [capacitance=4.7µF voltage=10V part_number="Murata GRM219R61A475KE19D" package="0805 [SMD, multilayer]"]
  ROC2 = Resistor [tolerance=±5% resistance=15M part_number="Digikey 541-15Majct-nd" package="0805 [SMD]"]
  ROC1 = Resistor [tolerance=±1% resistance=4.4M part_number="Digikey 541-4.42Mcct-nd" package="0805 [SMD]"]
  ROK3 = Resistor [tolerance=±1% resistance=4.8M part_number="Digikey 541-4.75Mcct-nd" package="0805 [SMD]"]
  ROK2 = Resistor [tolerance=±1% resistance=2.6M part_number="Digikey 541-2.61Mcct-nd" package="0805 [SMD]"]
  ROK1 = Resistor [tolerance=±1% resistance=2.6M part_number="Digikey 541-2.61Mcct-nd" package="0805 [SMD]"]
  Cvref = Ceramic Capacitor [capacitance=0.01µF voltage=50V part_number="Murata GRM188R71H103KA01D" package="0603 [SMD, multilayer]"]
  Load- = female pin header, 1 pin [form="♀ (female)"]
  GND = female pin header, 1 pin [form="♀ (female)"]
  BAT+ = female pin header, 1 pin [form="♀ (female)"]
  Cstor = Ceramic Capacitor [capacitance=4.7µF voltage=10V part_number="Murata GRM219R61A475KE19D" package="0805 [SMD, multilayer]"]
  Load+ = female pin header, 1 pin [form="♀ (female)"]
  VIN = female pin header, 1 pin [form="♀ (female)"]
  Gnd = female pin header, 1 pin [form="♀ (female)"]
  U1 = Mystery SMDSMD_4mm [part_number="22uH Coilcraft LPS4018-223MLB"]
  Pad1 = Pad [width=1 height=1 connect=center]
  part = Ceramic Capacitor [capacitance=100nF package="100 mil [THT, multilayer]"]  # not connected
  Cfltr = Ceramic Capacitor [capacitance=0.1µF voltage=50V part_number="std 0.1uF 50V" package="0603 [SMD, multilayer]"]
  Q1 = Basic_FET_P_Channel [part_number="Digikey FDN327NCT-ND"]

nets (from the pcb view):
  N1: IC1.connector0, IC1.connector4, IC1.connector11, IC1.connector12, Chvr.1, ROC1.Pin_0, ROK1.Pin_1, Cvref.0, GND.pin1, Cstor.0, Gnd.pin1, Cfltr.1, Q1.connector2
  N2: IC1.connector1, Chvr.0, ROC2.Pin_1, VIN.pin1, U1.connector0, Pad1.pad
  N3: IC1.connector2, ROC2.Pin_0, ROC1.Pin_1
  N4: IC1.connector3, Cvref.1
  N5: IC1.connector5, IC1.connector9, ROK2.Pin_1, ROK1.Pin_0
  N6: IC1.connector6, ROK3.Pin_0
  N7: IC1.connector7, IC1.connector8, ROK3.Pin_1, ROK2.Pin_0
  N8: IC1.connector10, Q1.connector0
  N9: IC1.connector13, BAT+.pin1
  N10: IC1.connector14, Cstor.1, Load+.pin1, Cfltr.0
  N11: IC1.connector15, U1.connector1
  N12: Load-.pin1, Q1.connector1
