# Fritzing sketch id938_brgogo_lcd_0 (saved by Fritzing 0.7.11b)
breadboards: 1

parts:
  LCD1 = LCD screen
  R1 = Resistor [tolerance=±5% resistance=220 package=THT]
  R2 = Trimmer Potentiometer [maximum_resistance=10kΩ package=THT]
  J1 = female pin header, 8 pins [form="♀ (female)"]
  J2 = female pin header, 8 pins [form="♀ (female)"]
  J3 = female pin header, 8 pins [form="♀ (female)"]
  J4 = female pin header, 8 pins [form="♀ (female)"]

nets:
  N1: LCD1.VSS, LCD1.R/W, LCD1.LED-, R2.leg2, J1.pin4
  N2: LCD1.VDD, R1.Pin_1, R2.leg1, J1.pin8
  N3: LCD1.V0, R2.wiper
  N4: LCD1.RS, J1.pin2
  N5: LCD1.E, J2.pin7
  N6: LCD1.DB4, J4.pin2
  N7: LCD1.DB5, J3.pin2
  N8: LCD1.DB6, J3.pin7
  N9: LCD1.DB7, J4.pin7
  N10: LCD1.LED+, R1.Pin_0
