# Fritzing sketch id941_br_gogo_bluetooth_serial_0 (saved by Fritzing 0.7.11b)
breadboards: 1

parts:
  R1 = Resistor [tolerance=±5% resistance=220 package=THT]
  C1 = Electrolytic Capacitor [capacitance=1µF package="100 mil [THT, electrolytic]"]
  Power_plug1 = Power plug
  IC1 = IC, DIP package, 16 pins [chip_label=Max232]
  D1 = Rectifier Diode [part_number=1N4001 package="300 mil [THT]"]
  D2 = Rectifier Diode [part_number=1N4001 package="300 mil [THT]"]
  J1 = female pin header, 9 pins [form="♀ (female)"]
  C2 = Electrolytic Capacitor [capacitance=1µF package="100 mil [THT, electrolytic]"]
  C3 = Electrolytic Capacitor [capacitance=1µF package="100 mil [THT, electrolytic]"]
  C4 = Electrolytic Capacitor [capacitance=1µF package="100 mil [THT, electrolytic]"]
  J5 = female pin header, 2 pins [form="♀ (female)"]
  J6 = female pin header, 1 pin [form="♀ (female)"]
  LED1 = LED - 3mm [color="Red (633nm)" package="3 mm [THT]"]
  J7 = screw terminal, 3 pins
  J8 = screw terminal, 3 pins

nets:
  N1: R1.Pin_0, LED1.anode
  N2: R1.Pin_1, C1.-, Power_plug1.VCC, D2.anode, J1.pin6, C2.+
  N3: C1.+, IC1.pin2
  N4: Power_plug1.GND, IC1.pin15, D1.anode, J6.pin1
  N5: IC1.pin1, C4.+
  N6: IC1.pin3, C4.-
  N7: IC1.pin4, C3.+
  N8: IC1.pin5, C3.-
  N9: IC1.pin6, C2.-
  N10: IC1.pin11, J5.pin2, J8.pin3
  N11: IC1.pin12, J5.pin1, J7.pin3
  N12: IC1.pin13, J1.pin3
  N13: IC1.pin14, J1.pin2
  N14: IC1.pin16, D2.cathode
  N15: D1.cathode, LED1.cathode
  N16: J1.pin7, J1.pin8

notes:
  sensor 4
  rx/tx
  TX
  RX
  Serial DB9
  5V
  sensor 5
