# Fritzing sketch id943_arduino_on_bd_0 (saved by Fritzing 0.9.2b)
breadboards: 1

parts:
  Bauteil1 = Breadboard Power Supply Board SMD
  U1 = atmega328 [package=dip]
  S1 = Momentary Switch [package=ksa_sealed_tac_switch]
  XTAL1 = Crystal [frequency="16 Mhz" package=THT]
  LED1 = LED - 5mm [color="Red (633nm)" package="5 mm [THT]"]  # not connected
  R1 = Resistor [tolerance=±5% resistance=220 package="1206 [SMD]"]
  C3 = Kondensator22pF
  C2 = Kondensator22pF

nets:
  GND: Bauteil1.GND, U1.GND, C3.connector1, C2.connector1
  VCC: Bauteil1.VCC, U1.VCC, U1.AVCC, U1.AREF
  N1: U1.XLAT1, XTAL1.pin_0, C2.connector0
  N2: U1.XLAT2, C3.connector0
  N3: U1.D5_(PWM), XTAL1.pin_1
  N4: U1.D9_(PWM), R1.Pin_1
  N5: U1.D13, R1.Pin_0
  N6: S1.1, S1.2
  N7: S1.3, S1.4
