# Fritzing sketch id944_rotation_0 (saved by Fritzing 0.7.12b)
breadboards: 1

parts:
  IC1 = IC, DIP package, 8 pins [chip_label=12F509 spacing=300mil]
  LED2 = LED - 5mm [color="Red (633nm)" package="5 mm [THT]"]
  R1 = Resistor [tolerance=±5% resistance=150 package=THT]
  C1 = Ceramic Capacitor [capacitance=100nF package="100 mil [THT, multilayer]"]
  J1 = male pin header, 5 pins [form="♂ (male)"]
  LED3 = LED - 5mm [color="Red (633nm)" package="5 mm [THT]"]
  LED4 = LED - 5mm [color="Red (633nm)" package="5 mm [THT]"]
  LED5 = LED - 5mm [color="Red (633nm)" package="5 mm [THT]"]
  LED6 = LED - 5mm [color="Red (633nm)" package="5 mm [THT]"]

nets:
  N1: IC1.pin1, R1.Pin_1, C1.0, J1.pin2
  N2: IC1.pin2, LED5.cathode
  N3: IC1.pin3, LED6.cathode
  N4: IC1.pin4, J1.pin1
  N5: IC1.pin5, LED4.cathode
  N6: IC1.pin6, LED2.cathode, J1.pin5
  N7: IC1.pin7, J1.pin4, LED3.cathode
  N8: IC1.pin8, C1.1, J1.pin3
  N9: LED2.anode, R1.Pin_0, LED3.anode, LED4.anode, LED5.anode, LED6.anode

notes:
  Breadboard ISP for PIC12F509
