# Fritzing sketch id945_Breadboard_USB_Power_0 (saved by Fritzing 0.7.1b)
breadboards: 1

parts:
  USB = USB connector [package=THT]
  LED1 = LED - 5mm [color="Red (633nm)" package="5 mm [THT]"]
  J1 = male pin header, 2 pins [form="♂ (male)"]
  J3 = male pin header, 2 pins [form="♂ (male)"]
  J4 = male pin header, 2 pins [form="♂ (male)"]
  R1 = Resistor [tolerance=±5% resistance=1k package=THT]
  J2 = male pin header, 2 pins [form="♂ (male)"]

nets:
  N1: USB.5V, LED1.anode, J1.pin1, J3.pin1, J4.pin1, J2.pin1
  N2: USB.GND, USB.chassis5, USB.chassis6, J1.pin2, J3.pin2, J4.pin2, R1.Pin_0, J2.pin2
  N3: LED1.cathode, R1.Pin_1

notes:
  Breadboard USB Power, Supply power to a regular sized breadboard with USB, 1.0
