# Fritzing sketch id947_ESP8266_Breakout_Board_0 (saved by Fritzing 0.9.1b)
stripboards: 1

parts:
  VCC1 = Battery
  J2 = double row rounded female pin header, 4 pins [form="♀ (female rounded)"]
  J3 = double row rounded female pin header, 4 pins [form="♀ (female rounded)"]
  part = ESP8266_module [part_number=ESP8266]
  UART_GND_RXD_NC_TXD = double row rounded female pin header, 4 pins [form="♀ (female rounded)"]
  Firmware_Update = Momentary Switch [package=ksa_sealed_tac_switch]
  Reset = Momentary Switch [package=ksa_sealed_tac_switch]
  R1 = Resistor [tolerance=±5% resistance=4.7k package=THT]
  DS1 = DS18B20 1-Wire Temperature Sensor [part_number=DS18B20]
  GPIO2_GPIO0_RXD_TXD_VCC_GND = screw terminal, 11 pins

nets:
  N1: VCC1.-, J2.pin1, part.connector6, UART_GND_RXD_NC_TXD.pin1, Firmware_Update.3, Firmware_Update.4, Reset.3, DS1.GND, GPIO2_GPIO0_RXD_TXD_VCC_GND.pin11
  N2: VCC1.+, J3.pin2, J3.pin4, part.connector1, part.connector5, R1.Pin_1, DS1.VDD, GPIO2_GPIO0_RXD_TXD_VCC_GND.pin9
  N3: J2.pin2, part.connector4, R1.Pin_0, DS1.DQ, GPIO2_GPIO0_RXD_TXD_VCC_GND.pin1
  N4: J2.pin3, part.connector2, Firmware_Update.1, GPIO2_GPIO0_RXD_TXD_VCC_GND.pin3
  N5: J2.pin4, part.connector0, UART_GND_RXD_NC_TXD.pin2, GPIO2_GPIO0_RXD_TXD_VCC_GND.pin5
  N6: J3.pin1, part.connector7, UART_GND_RXD_NC_TXD.pin4, GPIO2_GPIO0_RXD_TXD_VCC_GND.pin7
  N7: J3.pin3, part.connector3, Reset.1

notes:
  ESP8266 with DS18B20 Temperature Sensor
