# Fritzing sketch id948_SharpBreakoutboard_06.june.2014_0 (saved by Fritzing 0.8.7b)
circuit board: 2.6cm x 1.33cm
breadboards: 1

parts:
  J1 = female pin header, 3 pins [form="♀ (female)"]
  J3 = female pin header, 5 pins [form="♀ (female)"]
  C1 = Ceramic Capacitor [capacitance=100nF package="0805 [SMD, multilayer]"]
  R1 = Resistor [tolerance=±5% resistance=1 package="0805 [SMD]"]
  R2 = Resistor [tolerance=±5% resistance=220 package="0805 [SMD]"]
  LED = smd LED [color="Green (565nm)" package="1206 [SMD]"]
  J4 = female pin header, 1 pin [form="♀ (female)"]
  J5 = female pin header, 1 pin [form="♀ (female)"]

nets:
  GND: J1.pin1, J3.pin4, C1.0, R1.Pin_1, J4.pin1, J5.pin1
  VOUT: J1.pin2, J3.pin3, R2.Pin_1
  5V: J1.pin3, J3.pin1, LED.anode
  N1: J3.pin2, R1.Pin_0
  N2: J3.pin5, C1.1
  N3: R2.Pin_0, LED.cathode

notes:
  Sharp GP2Y0D340K IR sensor
  06.june 2014
  Frode Lillerud
  GND
  OUT
  5V
  (put sensor here)
  Breakoutboard for GP2Y0D340K , B
