# Fritzing sketch id949_attiny85_breathing_0 (saved by Fritzing 0.8.5b)
circuit board: 5cm x 3cm
breadboards: 1

parts:
  Q1 = MOSFET-NCHANNEL [package=sot23-3]
  LED1 = smd LED [color="Red (633nm)" package="0805 [SMD]"]
  Q2 = MOSFET-NCHANNEL [package=sot23-3]
  Q3 = MOSFET-NCHANNEL [package=sot23-3]
  Q4 = MOSFET-NCHANNEL [package=sot23-3]
  LED2 = smd LED [color="Red (633nm)" package="0805 [SMD]"]
  LED3 = smd LED [color="Red (633nm)" package="0805 [SMD]"]
  LED4 = smd LED [color="Red (633nm)" package="0805 [SMD]"]
  R4 = Resistor [tolerance=±5% resistance=220 package="0805 [SMD]"]
  R3 = Resistor [tolerance=±5% resistance=220 package="0805 [SMD]"]
  R2 = Resistor [tolerance=±5% resistance=220 package="0805 [SMD]"]
  R1 = Resistor [tolerance=±5% resistance=220 package="0805 [SMD]"]
  U1 = ATTINY13 [package=so]
  BAT1 = Battery Holders [package=battcom_20mm_pth]

nets:
  N1: Q1.G, Q2.G, Q3.G, Q4.G, U1.PB0(MOSI)
  GND: Q1.S, Q2.S, Q3.S, Q4.S, U1.GND, BAT1.-
  N2: Q1.D, LED1.cathode
  N3: LED1.anode, R1.Pin_1
  N4: Q2.D, LED2.cathode
  N5: Q3.D, LED3.cathode
  N6: Q4.D, LED4.cathode
  N7: LED2.anode, R2.Pin_1
  N8: LED3.anode, R3.Pin_1
  N9: LED4.anode, R4.Pin_1
  5V: R4.Pin_0, R3.Pin_0, R2.Pin_0, R1.Pin_0, U1.VCC, BAT1.+
