# Fritzing sketch id94_3faseRectifier_0 (saved by Fritzing 0.9.3b)
stripboards: 1

parts:
  D1 = Schottky Diode [part_number=1N5817 package="Melf DO-213 AB [SMD]"]
  D4 = Schottky Diode [part_number=1N5817 package="Melf DO-213 AB [SMD]"]
  D5 = Schottky Diode [part_number=1N5817 package="Melf DO-213 AB [SMD]"]
  D6 = Schottky Diode [part_number=1N5817 package="Melf DO-213 AB [SMD]"]
  D7 = Schottky Diode [part_number=1N5817 package="Melf DO-213 AB [SMD]"]
  D8 = Schottky Diode [part_number=1N5817 package="Melf DO-213 AB [SMD]"]
  C1 = Electrolytic Capacitor [capacitance=1µF package="100 mil [THT, electrolytic]"]
  C2 = Electrolytic Capacitor [capacitance=1µF package="100 mil [THT, electrolytic]"]

nets:
  N1: D1.cathode, D7.cathode, C1.+, C2.-
  N2: D1.anode, D4.cathode
  N3: D4.anode, D8.anode, C1.-, C2.+
  N4: D5.anode, D6.cathode
  N5: D7.anode, D8.cathode
