# Fritzing sketch id950_Brekina_VW_T1_0 (saved by Fritzing 0.9.3b)

parts:
  Onderdeel2 = Bluetooth HC-05 Macho
  LM1 = RioRand LM2596
  M1 = DC Motor  # not connected
  U1 = LIPO-2000mAh [package=lipo-2000]
  Onderdeel3 = PowerBoost 500 Charger
  Onderdeel1 = Arduino Nano (Rev3.0)
  IC1 = L293D [package=THT]
  S1 = Toggle Switch [package=THT]
  J1 = Power Jack [package=power_jack_smd]
  JP1 = USB_MICROB_PLUG [package=micro-b-th]

nets:
  N1: Onderdeel2.TXD, Onderdeel1.D0/RX
  N2: Onderdeel2.RXD, Onderdeel1.D1/TX
  VCC: Onderdeel2.VCC, Onderdeel1.5V, S1.L1
  GND: Onderdeel2.GND, Onderdeel3.GND, Onderdeel1.GND
  N3: LM1.Pin_2, IC1.+Vmotor
  N4: U1.+, Onderdeel3.VBAT_IN
  N5: U1.-, Onderdeel3.GND_BAT_IN
  N6: Onderdeel3.5.0V, S1.COM
  N7: J1.PWR, JP1.VCC
  GND_2: J1.GND, JP1.GND
