# Fritzing sketch id951_BrewBotShield_0 (saved by Fritzing 0.9.3b)
circuit board: 6.86947cm x 5.35954cm
breadboards: 1

parts:
  R1 = Resistor [tolerance=±5% resistance=220 package=THT]
  R2 = Resistor [tolerance=±5% resistance=220 package=THT]
  R3 = Resistor [tolerance=±5% resistance=220 package=THT]
  R4 = Resistor [tolerance=±5% resistance=220 package=THT]
  R5 = Resistor [tolerance=±5% resistance=220 package=THT]
  R6 = Resistor [tolerance=±5% resistance=4.7 package=THT]
  LED1 = LED - 5mm [color="Green (560nm)" package="5 mm [THT]"]
  LED2 = LED - 5mm [color="Green (560nm)" package="5 mm [THT]"]
  LED3 = LED - 5mm [color="Green (560nm)" package="5 mm [THT]"]
  LED4 = LED - 5mm [color="Green (560nm)" package="5 mm [THT]"]
  LED5 = LED - 5mm [color="Red (633nm)" package="5 mm [THT]"]
  JP1 = Header 3 [package=molex-1x3_lock]
  JP2 = Header 3 [package=molex-1x3_lock]
  JP3 = Header 3 [package=molex-1x3_lock]
  JP4 = Header 3 [package=molex-1x3_lock]
  JP5 = Header 2 [package=molex-1x2_lock]
  JP6 = Header 2 [package=molex-1x2_lock]
  JP7 = Header 2 [package=molex-1x2_lock]
  JP8 = Header 2 [package=molex-1x2_lock]
  Part1 = Arduino Uno (Rev3)
  Part2 = Bluetooth HC-05 Macho

nets:
  N1: R1.Pin_0, Part1.D3_PWM
  N2: R1.Pin_1, LED2.anode
  N3: R2.Pin_0, Part1.D4
  N4: R2.Pin_1, LED3.anode
  N5: R3.Pin_0, Part1.D5_PWM
  N6: R3.Pin_1, LED4.anode
  N7: R4.Pin_0, Part1.D6_PWM
  N8: R4.Pin_1, LED1.anode
  N9: R5.Pin_0, Part1.D7
  N10: R5.Pin_1, LED5.anode
  N11: R6.Pin_0, JP1.2, JP2.2, JP3.2, JP4.2, Part1.D2
  5V: R6.Pin_1, JP1.1, JP2.1, JP3.1, JP4.1, Part1.5V, Part2.VCC
  N12: LED1.cathode, JP8.1
  N13: LED2.cathode, JP7.1
  N14: LED3.cathode, JP5.1
  N15: LED4.cathode, JP6.1
  GND: LED5.cathode, JP1.3, JP2.3, JP3.3, JP4.3, JP5.2, JP6.2, JP7.2, JP8.2, Part1.GND, Part2.GND
  N16: Part1.D8, Part2.RXD
  N17: Part1.D9_PWM, Part2.TXD
