# Fritzing sketch id952_Brewpi_Shield_with_lcd_v1_0 (saved by Fritzing 0.9.1b)
circuit board: 6.88566cm x 5.36311cm

parts:
  R2 = Rotary Potentiometer (Large) [maximum_resistance=10kΩ package=THT]
  R1 = 4.7k resistor
  Part1 = Arduino Prototyping Shield
  LCD1 = LCD screen
  R3 = 10k resistor
  U1 = 74HC595 SMD [package="SO16 [SMD]"]
  C1 = 1uf
  C2 = 1uf
  R4 = 10k resistor
  R5 = 10k resistor
  R6 = 10k resistor
  C3 = 1uf
  C4 = 1uf
  C5 = 1uf

nets:
  GND: R2.leg1, Part1.GND, Part1.N$41, Part1.N$42, Part1.N$85, Part1.N$86, Part1.N$105, Part1.N$165, Part1.N$321, Part1.N$322, Part1.N$324, Part1.N$325, Part1.N$329, Part1.N$332, Part1.N$412, Part1.N$421, LCD1.VSS, LCD1.R/W, LCD1.LED-, U1.GND, U1.OE, C1.connector1, C2.connector1, C3.connector1, C4.connector1, C5.connector1
  N1: R2.wiper, LCD1.V0
  +5V: R2.leg2, R1.connector1, Part1.+5V, Part1.N$34, Part1.N$118, Part1.N$189, Part1.N$238, Part1.N$323, Part1.N$397, Part1.N$401, Part1.N$404, Part1.N$426, LCD1.VDD, R3.connector0, U1.VCC, C1.connector0, C2.connector0, R4.connector1, R5.connector1, R6.connector1
  N2: R1.connector0, Part1.A4
  N3: Part1.D13, Part1.N$62, U1.SH_CP
  N4: Part1.D8, Part1.N$409, R5.connector0, C4.connector0
  N5: Part1.D9, Part1.N$410, R6.connector0, C5.connector0
  N6: Part1.D10, Part1.N$72, U1.ST_CP
  N7: Part1.D11, Part1.N$77, U1.DS
  N8: Part1.N$37, U1.Q7'
  N9: Part1.N$40, LCD1.LED+
  N10: Part1.N$48, R3.connector1, U1.MR
  N11: Part1.N$54, Part1.N$55, LCD1.DB7, U1.Q7
  N12: Part1.N$65, Part1.N$66, LCD1.DB6, U1.Q6
  N13: Part1.N$67, U1.Q2
  N14: Part1.N$76, LCD1.RS, U1.Q0
  N15: Part1.N$78, Part1.N$79, LCD1.DB5, U1.Q5
  N16: Part1.N$84, Part1.N$90, LCD1.DB4, U1.Q4
  N17: Part1.N$87, U1.Q3
  N18: Part1.N$178, Part1.N$190, LCD1.E, U1.Q1
  N19: Part1.N$422, R4.connector0, C3.connector0
