# Fritzing sketch id953_Bright_Ball_IOT_0 (saved by Fritzing 0.9.0b)
breadboards: 1

parts:
  R4 = Resistor [tolerance=±5% resistance=470 package=THT]
  S2 = Pushbutton [package="[THT]"]
  S3 = Pushbutton [package="[THT]"]
  S4 = Pushbutton [package="[THT]"]
  U1 = LCD-16X2 [package=lcd-16x2]
  LCM1602_IIC2 = generic_ic_dip_22_300mil.fzp [part_number="LCM1602 IIC" chip_label="LCM1602 IIC"]
  NEOPIXEL2 = Neopixel_Strip____Black__30_m
  D3 = Rectifier Diode [part_number=1N4001 package="300 mil [THT]"]
  RHT3 = Humidity and Temperature Sensor RHT03
  S5 = Toggle Switch [package=THT]
  Componente6 = Arduino Uno (Rev3)
  D6 = Rectifier Diode [part_number=1N4001 package="300 mil [THT]"]
  R5 = Resistor [tolerance=±5% resistance=1k package=THT]
  Componente8 = Real Time Clock Module - DS1307 RTC Breakout Board
  U6 = ESP8266_module [part_number=ESP8266]
  U7 = V_REG_LD1117VXX [package=78xxl]
  Componente9 = DC-DC 5v (bottom)
  Power_plug3 = Power plug
  D7 = Rectifier Diode [part_number=1N4001 package="300 mil [THT]"]
  R6 = Resistor [tolerance=±5% resistance=512 package=THT]
  R7 = Resistor [tolerance=±5% resistance=270 package=THT]

nets:
  N1: R4.Pin_0, Componente6.D9_PWM
  GND: S2.Pin_1, S2.Pin_2, S3.Pin_1, S3.Pin_2, S4.Pin_1, S4.Pin_2, LCM1602_IIC2.connector16, NEOPIXEL2.connector3, RHT3.GND_2, S5.L1, Componente6.GND, Componente8.GND, U6.connector6, U7.GND, Componente9.connector4, R6.Pin_1
  N2: S2.Pin_3, S2.Pin_4, Componente6.D6_PWM
  N3: S3.Pin_3, S3.Pin_4, Componente6.D7
  N4: S4.Pin_3, S4.Pin_4, Componente6.D8
  N5: U1.VSS, LCM1602_IIC2.connector0
  N6: U1.VDD, LCM1602_IIC2.connector1
  N7: U1.VO, LCM1602_IIC2.connector2
  N8: U1.RS, LCM1602_IIC2.connector3
  N9: U1.R_W, LCM1602_IIC2.connector4
  N10: U1.E, LCM1602_IIC2.connector5
  N11: U1.DB0, LCM1602_IIC2.connector6
  N12: U1.DB1, LCM1602_IIC2.connector7
  N13: U1.DB2, LCM1602_IIC2.connector8
  N14: U1.DB3, LCM1602_IIC2.connector9
  N15: U1.DB4, LCM1602_IIC2.connector10
  N16: U1.DB5, LCM1602_IIC2.connector11
  N17: U1.DB6, LCM1602_IIC2.connector12
  N18: U1.DB7, LCM1602_IIC2.connector13
  N19: U1.A, LCM1602_IIC2.connector14
  N20: U1.K, LCM1602_IIC2.connector15
  5V: LCM1602_IIC2.connector17, RHT3.Vcc, S5.L2, Componente6.5V, D6.cathode, R5.Pin_1, Componente8.5V, U7.IN
  N21: LCM1602_IIC2.connector18, Componente6.A4/SDA, Componente8.SDA
  N22: LCM1602_IIC2.connector19, Componente6.A5/SCL, Componente8.SCL
  N23: NEOPIXEL2.connector1, D3.cathode
  N24: D3.anode, D6.anode, Componente9.connector3
  N25: RHT3.Data-signal, Componente6.D4, R5.Pin_0
  N26: S5.COM, Componente6.D12/MISO
  N27: Componente6.D2, U6.connector0
  N28: Componente6.D3_PWM, R6.Pin_0, R7.Pin_1
  N29: U6.connector1, U6.connector5, U7.OUT
  N30: U6.connector7, R7.Pin_0
  N31: Componente9.connector0, D7.cathode
  N32: Componente9.connector1, Power_plug3.GND
  N33: Power_plug3.VCC, D7.anode
