# Fritzing sketch id954_brillo3LED_potenciometro_0 (saved by Fritzing 0.9.2b)
breadboards: 1

parts:
  Parte1 = Arduino Uno (Rev3)
  LED1 = LED - 5mm [color="Green (570nm)" package="5 mm [THT]"]
  R2 = Resistor [tolerance=±5% resistance=220 package=THT]
  LED2 = LED - 5mm [color="Red (633nm)" package="5 mm [THT]"]
  LED3 = LED - 5mm [color="Yellow (592nm)" package="5 mm [THT]"]
  R3 = Resistor [tolerance=±5% resistance=220 package=THT]
  R4 = Resistor [tolerance=±5% resistance=220 package=THT]
  R5 = Rotary Potentiometer (Small) [maximum_resistance=100kΩ package=THT]

nets:
  N1: Parte1.A0, R5.wiper
  N2: Parte1.D9_PWM, LED1.anode
  N3: Parte1.D10_PWM/SS, LED2.anode
  N4: Parte1.D11_PWM/MOSI, LED3.anode
  N5: Parte1.GND, R2.Pin_1, R3.Pin_1, R4.Pin_1, R5.leg2
  N6: Parte1.5V, R5.leg1
  N7: LED1.cathode, R2.Pin_0
  N8: LED2.cathode, R3.Pin_0
  N9: LED3.cathode, R4.Pin_0
