# Fritzing sketch id957_POTENCIOMETRooooo_0 (saved by Fritzing 0.9.2b)
breadboards: 1

parts:
  Parte1 = Arduino Uno (Rev3)
  LED1 = LED - 5mm [color="Red (633nm)" package="5 mm [THT]"]
  R2 = Rotary Potentiometer (Small) [maximum_resistance=100kΩ package=THT]
  R3 = Resistor [tolerance=±5% resistance=220 package=THT]

nets:
  N1: Parte1.A0, R2.wiper
  N2: Parte1.D9_PWM, LED1.anode
  N3: Parte1.5V, R2.leg1
  N4: Parte1.GND, R2.leg2, R3.Pin_1
  N5: LED1.cathode, R3.Pin_0

notes:
  Led _Potenciometro
