# Fritzing sketch id958_BT_HC_05_0 (saved by Fritzing 0.9.3b)
breadboards: 1

parts:
  Composant1 = Arduino Uno (Rev3)
  Composant2 = Bluetooth HC-05 Macho  # not connected
  LED1 = LED - 5mm [color="Blue (505nm)" package="5 mm [THT]"]

nets:
  N1: Composant1.GND, LED1.cathode

notes:
  HC-08
  STATE : LED
  RXD : D10
  TXD : D11
  GND : GND
  VCC : 5V
  EN(KEY) : D9
