# Fritzing sketch id959_BT_HC_08_0 (saved by Fritzing 0.9.3b)
breadboards: 1

parts:
  Composant1 = Arduino Uno (Rev3)
  Composant2 = Bluetooth HC-05 Macho  # not connected
  LED1 = LED - 5mm [color="Blue (430nm)" package="5 mm [THT]"]
  LED2 = LED - 5mm [color="Red (633nm)" package="5 mm [THT]"]

nets:
  N1: Composant1.D9_PWM, Composant1.GND, LED1.cathode, LED2.anode

notes:
  HC-08
  STATE : LED bleue
  RXD : D11 (Tx Arduino)
  TXD : D10 (RX Arduino)
  GND : GND
  VCC : D12 (Gestion mode AT)
  EN(KEY) : D9 (Gestion mode AT)
  LED rouge (mode AT)
