# Fritzing sketch id95_3ledRotation_0 (saved by Fritzing 0.8.7b)
breadboards: 1

parts:
  Part2 = Arduino Nano (Rev3.0)
  LED3 = LED - 5mm [color="Green (555nm)" package="5 mm [THT]"]
  LED4 = LED - 5mm [color="Red (633nm)" package="5 mm [THT]"]
  R4 = Resistor [tolerance=±5% resistance=220 package=THT]
  R5 = Resistor [tolerance=±5% resistance=220 package=THT]
  S2 = Pushbutton [package="[THT]"]
  R6 = Resistor [tolerance=±5% resistance=10k package=THT]

nets:
  N1: Part2.GND, LED3.anode, LED4.anode, R6.Pin_1
  N2: Part2.D2, S2.Pin_3, S2.Pin_4, R6.Pin_0
  N3: Part2.D11/MOSI, R5.Pin_0
  N4: Part2.D12/MISO, R4.Pin_1
  N5: Part2.5V, S2.Pin_1, S2.Pin_2
  N6: LED3.cathode, R4.Pin_0
  N7: LED4.cathode, R5.Pin_1

notes:
  Ardunio test LED along with 2 other LED's flash in rotation. When the button is pushed the current LED in the rotation goes solid and the other 2 blink.
  //Stop rotation on current LED
  int speed = 500;
  int step = -50;
  void setup() {
  pinMode(13,OUTPUT);
  pinMode(12,OUTPUT);
  pinMode(11,OUTPUT);
  pinMode(2,INPUT);
  }
  void loop() {
  turnOnLED(11, speed);
  turnOnLED(12, speed);
  turnOnLED(13, speed);
  if (speed < 40) step = 50;
  else if (speed < 80) step = -5;
  else if (speed > 500) step = -50;
  speed = speed + step;
  }
  int turnOnLED(int LED, int forDelay) {
  digitalWrite(13,LOW);
  digitalWrite(12,LOW);
  digitalWrite(11,LOW);
  digitalWrite(LED,HIGH);
  delay(forDelay);
  if (digitalRead(2) == HIGH)
  {
  blinkOthers(LED, forDelay);
  }
  return 0;
  }
  void blinkOthers(int LED, int forDelay) {
  int ledOne = LED == 11 ? 12 : 11;
  int ledTwo = LED == 13 ? 12 : 13;
  while (digitalRead(2) == HIGH)
  {
  digitalWrite(ledOne,HIGH);
  digitalWrite(ledTwo,HIGH);
  delay(forDelay);
  digitalWrite(ledOne,LOW);
  digitalWrite(ledTwo,LOW);
  delay(forDelay);
  }
  }
