# Fritzing sketch id960_5V_voltagereg_0 (saved by Fritzing 0.9.3b)
breadboards: 1

parts:
  VCC1 = Battery block 9V
  U1 = Voltage Regulator - 5V [package="TO220 [THT]"]
  C1 = Electrolytic Capacitor [capacitance=10µF voltage=16V package="100 mil [THT, electrolytic]"]
  C2 = Electrolytic Capacitor [capacitance=1µF voltage=16V package="100 mil [THT, electrolytic]"]

nets:
  N1: VCC1.-, U1.GND, C1.-, C2.-
  N2: VCC1.+, U1.input_voltage, C1.+
  N3: U1.output_voltage, C2.+
