# Fritzing sketch id961_Burglar_Alarm_0 (saved by Fritzing 0.9.1b)
breadboards: 1

parts:
  Part1 = Arduino Uno (Rev3)
  R1 = Resistor [tolerance=±5% resistance=220 package=THT]
  S1 = Tilt Switch [package=THT]
  J1 = Piezo Speaker
  LED1 = LED - 5mm [color="Red (633nm)" package="5 mm [THT]"]
  LED2 = LED - 5mm [color="Red (633nm)" package="5 mm [THT]"]
  LED3 = LED - 5mm [color="Red (633nm)" package="5 mm [THT]"]  # not connected

nets:
  N1: Part1.D9_PWM, R1.Pin_0
  N2: Part1.GND, S1.Pin_1
  N3: R1.Pin_1, J1.pin1, LED1.anode, LED2.anode
  N4: S1.Pin_2, J1.pin2, LED1.cathode, LED2.cathode
