# Fritzing sketch id962_Untitled_Sketch_0 (saved by Fritzing 0.9.3b)
breadboards: 1

parts:
  Part1 = Arduino Mega 2560 (Rev3)
  LED1 = LED - 5mm [color="Red (633nm)" package="5 mm [THT]"]
  LED2 = LED - 5mm [color="Yellow (595nm)" package="5 mm [THT]"]
  R2 = Trimmer Potentiometer [maximum_resistance=10kΩ package=THT]
  S1 = Pushbutton [package="[THT]"]
  R3 = Resistor [tolerance=±5% resistance=10k package=THT]
  R4 = Resistor [tolerance=±5% resistance=220 package=THT]
  R5 = Resistor [tolerance=±5% resistance=220 package=THT]
  LCD1 = LCD screen
  7_Segment1 = 7 Segment Display
  7_Segment2 = 7 Segment Display  # not connected
  7_Segment3 = 7 Segment Display  # not connected
  7_Segment4 = 7 Segment Display  # not connected
  7_Segment5 = 7 Segment Display  # not connected
  7_Segment6 = 7 Segment Display  # not connected
  7_Segment7 = 7 Segment Display  # not connected
  7_Segment8 = 7 Segment Display  # not connected
  R6 = Rotary Potentiometer (Small) [maximum_resistance=100kΩ package=THT]
  RE1 = Rotary Encoder [package=THT]
  RE2 = Rotary Encoder [package=THT]
  RE3 = Rotary Encoder [package=THT]

nets:
  N1: Part1.D11_PWM, S1.Pin_3, S1.Pin_4, R3.Pin_1
  N2: Part1.D10_PWM, RE1.EncoderPinB, RE2.EncoderPinC, RE3.EncoderPinA
  N3: Part1.D9_PWM, RE2.EncoderPinB, RE3.EncoderPinC
  N4: Part1.D8_PWM, RE3.EncoderPinB
  5V: Part1.5V, R2.leg2, S1.Pin_1, S1.Pin_2, LCD1.VDD, 7_Segment1.Segment_G, R6.leg2, RE1.EncoderPinC, RE2.EncoderPinA
  GND: Part1.GND, R2.leg1, R3.Pin_0, R4.Pin_1, R5.Pin_1, LCD1.VSS, LCD1.LED-, 7_Segment1.Segment_F, R6.leg1, RE1.EncoderPinA
  N5: Part1.D2_PWM, LCD1.RS
  N6: Part1.D3_PWM, LCD1.R/W
  N7: Part1.D4_PWM, LCD1.DB4
  N8: Part1.D5_PWM, LCD1.DB5
  N9: Part1.D6_PWM, LCD1.DB6
  N10: Part1.D7_PWM, LCD1.DB7
  N11: Part1.D24, LED1.anode
  N12: Part1.D46, 7_Segment1.common_anode
  N13: Part1.D48, 7_Segment1.Segment_D
  N14: Part1.D50, 7_Segment1.Segment_E
  N15: LED1.cathode, R4.Pin_0
  N16: LED2.cathode, R5.Pin_0
  N17: LED2.anode, LCD1.LED+, R6.wiper
