# Fritzing sketch id964_bus_notifier_0 (saved by Fritzing 0.8.5b)
breadboards: 1

parts:
  R3 = Resistor [tolerance=±5% resistance=220 package=THT]
  Raspberry_Pi_B_rev1 = Raspberry Pi B rev2
  Contrast2 = Rotary Potentiometer (Small) [maximum_resistance=100kΩ]
  LCD2 = LCD screen
  Button_right = Arcade_Button__blue
  Button_left = Arcade_Button__red

nets:
  N1: R3.Pin_0, LCD2.LED+
  5V: R3.Pin_1, Raspberry_Pi_B_rev1.5V, Contrast2.leg2, LCD2.VDD
  GND: Raspberry_Pi_B_rev1.GND, Contrast2.leg1, LCD2.VSS, LCD2.R/W, LCD2.LED-, Button_right.connector2, Button_left.connector2
  N2: Raspberry_Pi_B_rev1.GPIO_23, LCD2.E
  N3: Raspberry_Pi_B_rev1.GPIO_18, Button_left.connector1
  N4: Raspberry_Pi_B_rev1.GPIO_22, LCD2.RS
  N5: Raspberry_Pi_B_rev1.GPIO_4, Button_right.connector1
  N6: Raspberry_Pi_B_rev1.GPIO_9, LCD2.DB4
  N7: Raspberry_Pi_B_rev1.GPIO_25, LCD2.DB5
  N8: Raspberry_Pi_B_rev1.GPIO_11, LCD2.DB6
  N9: Raspberry_Pi_B_rev1.GPIO_8, LCD2.DB7
  N10: Contrast2.wiper, LCD2.V0
