# Fritzing sketch id966_sem_project2_0 (saved by Fritzing 0.9.2b)
breadboards: 1
perfboards: 4

parts:
  IC1 = IC, DIP package, 20 pins [chip_label="IC 74LS241"]
  Part3 = Arduino Uno (Rev3)
  U1 = LCD-16X2 [package=lcd-16x2]
  J2 = shrouded pin header, 8 pins [form="♂ (shrouded male)"]
  J3 = Screw terminal - 2 pins [package=THT]
  J4 = Screw terminal - 2 pins [package=THT]
  IC2 = IC, DIP package, 16 pins [chip_label="driver motor"]  # not connected
  J5 = shrouded pin header, 8 pins [form="♂ (shrouded male)"]
  J6 = Screw terminal - 2 pins [package=THT]
  J7 = Screw terminal - 2 pins [package=THT]
  IC3 = IC, DIP package, 16 pins [chip_label="driver motor"]  # not connected
  J8 = shrouded pin header, 8 pins [form="♂ (shrouded male)"]
  J9 = shrouded pin header, 8 pins [form="♂ (shrouded male)"]
  J10 = Screw terminal - 2 pins [package=THT]
  J11 = Screw terminal - 2 pins [package=THT]  # not connected
  J12 = Screw terminal - 2 pins [package=THT]
  J13 = Screw terminal - 2 pins [package=THT]
  IC4 = IC, DIP package, 16 pins [chip_label="driver motor"]  # not connected
  IC5 = IC, DIP package, 16 pins [chip_label="driver motor"]  # not connected
  M1 = DC Motor
  M2 = DC Motor
  M3 = DC Motor  # not connected
  M4 = DC Motor
  J14 = Basic Servo
  J15 = Basic Servo
  R1 = Trimmer Potentiometer [maximum_resistance=10kΩ package=THT]
  VCC1 = 4 x AAA Battery Mount
  U3 = LIPO-2000mAh [package=lipo-2000]
  U4 = prefix0012

nets:
  N1: IC1.pin1, IC1.pin19
  N2: IC1.pin2, IC1.pin3
  VCC: IC1.pin20, Part3.5V, U1.VDD, J2.pin3, J2.pin8, J5.pin3, J5.pin8, J14.vcc, J15.vcc, VCC1.+
  N3: Part3.A0, J14.pulse
  N4: Part3.A1, J15.pulse
  N5: Part3.A2, U1.DB4
  N6: Part3.A3, U1.DB5
  N7: Part3.A4/SDA, U1.DB6
  N8: Part3.A5/SCL, U1.DB7
  N9: Part3.D8, U1.E
  N10: Part3.D9_PWM, U1.RS
  N11: Part3.D11_PWM/MOSI, J2.pin5
  N12: Part3.D12/MISO, J2.pin4
  N13: Part3.D2, J5.pin5
  N14: Part3.D3_PWM, J5.pin4
  N15: Part3.D4, J9.pin5
  N16: Part3.D5_PWM, J9.pin4
  N17: Part3.D6_PWM, J8.pin4
  N18: Part3.D7, J8.pin5
  GND: Part3.GND, U1.VSS, U1.R_W, J5.pin1, J8.pin1, J9.pin1, J14.gnd, J15.gnd, VCC1.-
  N19: U1.VO, R1.wiper
  N20: J3.pin1, M2.pin_2
  N21: J3.pin2, M2.pin_1
  N22: J4.pin1, J7.pin1
  N23: J4.pin2, J7.pin2, J12.pin2, J13.pin2, U3.-, U4.connector1
  N24: J6.pin1, M1.pin_2
  N25: J6.pin2, M1.pin_1
  N26: J8.pin3, J8.pin8
  N27: J9.pin3, J9.pin8
  N28: J10.pin1, M4.pin_2
  N29: J10.pin2, M4.pin_1
  N30: J12.pin1, J13.pin1, U3.+
