# Fritzing sketch id969_ButtonDHT11_0 (saved by Fritzing 0.9.3b)
breadboards: 1

parts:
  Part1 = Arduino Uno (Rev3)
  S1 = Momentary Switch [package=ksa_sealed_tac_switch]
  R1 = Resistor [tolerance=±5% resistance=220 package="2010 [SMD]"]
  LED1 = smd LED [color="Red (635nm)" package="0603 [SMD]"]
  RHT1 = Humidity and Temperature Sensor RHT03
  R2 = Resistor [tolerance=±5% resistance=220 package="2010 [SMD]"]

nets:
  N1: Part1.A0, RHT1.Vcc
  N2: Part1.D13/SCK, LED1.anode
  N3: Part1.D4, S1.4, R2.Pin_1
  N4: Part1.5V, S1.2, RHT1.Data-signal
  N5: Part1.GND, R1.Pin_0, RHT1.GND_2, R2.Pin_0
  N6: R1.Pin_1, LED1.cathode
