# Fritzing sketch id970_Button_led_fritzing_0 (saved by Fritzing 0.9.3b)
breadboards: 1

parts:
  LED1 = smd LED [color="Red (633nm)" package="1206 [SMD]"]
  S1 = Momentary Switch [package=ksa_sealed_tac_switch]
  부품1 = Arduino Uno (Rev3)
  R1 = Resistor [tolerance=±5% resistance=220 package=THT]
  R2 = Resistor [tolerance=±5% resistance=220 package=THT]

nets:
  N1: LED1.cathode, 부품1.GND, R2.Pin_1
  N2: LED1.anode, R1.Pin_0
  N3: S1.2, 부품1.D2, R2.Pin_0
  N4: S1.4, 부품1.5V
  N5: 부품1.D13/SCK, R1.Pin_1
