# Fritzing sketch id971_Button_piezo_fritzing_0 (saved by Fritzing 0.9.3b)
breadboards: 1

parts:
  S1 = Momentary Switch [package=ksa_sealed_tac_switch]
  부품1 = Arduino Uno (Rev3)
  R2 = Resistor [tolerance=±5% resistance=220 package=THT]
  J1 = Piezo Speaker

nets:
  N1: S1.2, 부품1.D2, R2.Pin_0
  N2: S1.4, 부품1.5V
  N3: 부품1.D8, J1.pin2
  N4: 부품1.GND, R2.Pin_1, J1.pin1
