# Fritzing sketch id972_buttons_test_fritz_1_0 (saved by Fritzing 0.9.2b)
stripboards: 1

parts:
  Part1 = Arduino Uno (Rev3)
  S1 = Pushbutton [package="[THT]"]
  S2 = Pushbutton [package="[THT]"]
  S3 = Pushbutton [package="[THT]"]
  S4 = Pushbutton [package="[THT]"]
  S5 = Pushbutton [package="[THT]"]
  S6 = Pushbutton [package="[THT]"]
  S7 = Pushbutton [package="[THT]"]
  S8 = Pushbutton [package="[THT]"]
  S9 = Pushbutton [package="[THT]"]
  S10 = Pushbutton [package="[THT]"]
  S11 = Pushbutton [package="[THT]"]
  R1 = Resistor [tolerance=±5% resistance=220 package=THT]
  R2 = Resistor [tolerance=±5% resistance=220 package=THT]
  R3 = Resistor [tolerance=±5% resistance=220 package=THT]
  R4 = Resistor [tolerance=±5% resistance=220 package=THT]
  R5 = Resistor [tolerance=±5% resistance=220 package=THT]
  R6 = Resistor [tolerance=±5% resistance=220 package=THT]
  R7 = Resistor [tolerance=±5% resistance=220 package=THT]
  R8 = Resistor [tolerance=±5% resistance=220 package=THT]
  R9 = Resistor [tolerance=±5% resistance=220 package=THT]
  R10 = Resistor [tolerance=±5% resistance=220 package=THT]
  R11 = Resistor [tolerance=±5% resistance=220 package=THT]

nets:
  N1: Part1.A0, S1.Pin_3, S1.Pin_4, S2.Pin_3, S2.Pin_4, S3.Pin_3, S3.Pin_4, S4.Pin_3, S4.Pin_4, S5.Pin_3, S5.Pin_4, S6.Pin_3, S6.Pin_4, S7.Pin_3, S7.Pin_4, S8.Pin_3, S8.Pin_4, S9.Pin_3, S9.Pin_4, S10.Pin_3, S10.Pin_4, S11.Pin_3, S11.Pin_4
  N2: Part1.5V, R1.Pin_1, R2.Pin_1, R3.Pin_1, R4.Pin_1, R5.Pin_1, R6.Pin_1, R7.Pin_1, R8.Pin_1, R9.Pin_1, R10.Pin_1, R11.Pin_1
  N3: S1.Pin_1, S1.Pin_2, R1.Pin_0
  N4: S2.Pin_1, S2.Pin_2, R2.Pin_0
  N5: S3.Pin_1, S3.Pin_2, R3.Pin_0
  N6: S4.Pin_1, S4.Pin_2, R4.Pin_0
  N7: S5.Pin_1, S5.Pin_2, R5.Pin_0
  N8: S6.Pin_1, S6.Pin_2, R6.Pin_0
  N9: S7.Pin_1, S7.Pin_2, R7.Pin_0
  N10: S8.Pin_1, S8.Pin_2, R8.Pin_0
  N11: S9.Pin_1, S9.Pin_2, R9.Pin_0
  N12: S10.Pin_1, S10.Pin_2, R10.Pin_0
  N13: S11.Pin_1, S11.Pin_2, R11.Pin_0
