# Fritzing sketch id974_kadai_0 (saved by Fritzing 0.9.3b)
breadboards: 1

parts:
  Part1 = Arduino Uno (Rev3)
  U1 = SLIDER [package=slider]
  J1 = Basic Force Sensing Resistor (FSR) [package=THT]
  R1 = Resistor [tolerance=±5% resistance=220 package="2512 [SMD]"]
  R2 = Resistor [tolerance=±5% resistance=220 package="2512 [SMD]"]
  J2 = Piezo Speaker

nets:
  N1: Part1.A0, J1.pin_0, R1.Pin_1
  N2: Part1.A1, U1.S
  N3: Part1.D5_PWM, R2.Pin_1
  N4: Part1.5V, U1.A, R1.Pin_0
  N5: U1.E, J1.pin_1, J2.pin1
  N6: R2.Pin_0, J2.pin2
