# Fritzing sketch id975_Assignment_1_0 (saved by Fritzing 0.9.3b)
circuit board: 8.46667cm x 5.64444cm
breadboards: 1

parts:
  J1 = Piezo Speaker
  D1 = Diode [package=diode-1n4148]
  Part1 = Ethernet Pro
  R1 = Resistor [tolerance=±5% resistance=220 package="2512 [SMD]"]
  Q1 = PNP-Transistor [package="TO92 [THT]"]
  M1 = DC Motor

nets:
  N1: J1.pin1, Part1.IO8
  N2: J1.pin2, Part1.GND, Q1.E
  N3: D1.A, Q1.C, M1.pin_2
  N4: D1.C, Part1.5V, M1.pin_1
  N5: Part1.IO9, R1.Pin_1
  N6: R1.Pin_0, Q1.B
