# Fritzing sketch id976_Quad_Pot_LEDs_0 (saved by Fritzing 0.9.2b)
circuit board: 14.4403cm x 9.92481cm
breadboards: 1

parts:
  Part1 = Arduino Nano (Rev3.0)
  R1 = Rotary Potentiometer (Small) [maximum_resistance=10kΩ package=THT]
  R2 = Rotary Potentiometer (Small) [maximum_resistance=10kΩ package=THT]
  R3 = Rotary Potentiometer (Small) [maximum_resistance=10kΩ package=THT]
  S2 = Pushbutton [package="[THT]"]
  R4 = Rotary Potentiometer (Small) [maximum_resistance=10kΩ package=THT]
  C1 = Electrolytic Capacitor [capacitance=1mF package="100 mil [THT, electrolytic]"]
  S3 = Pushbutton [package="[THT]"]
  R7 = Resistor [tolerance=±5% resistance=10k package=THT]
  R8 = Resistor [tolerance=±5% resistance=10k package=THT]
  R9 = Resistor [tolerance=±5% resistance=10k package=THT]
  J1 = female pin header, 2 pins [form="♀ (female)"]
  J2 = female pin header, 2 pins [form="♀ (female)"]
  J3 = female pin header, 2 pins [form="♀ (female)"]  # not connected
  S4 = Pushbutton [package="[THT]"]
  R10 = Resistor [tolerance=±5% resistance=330 package=THT]  # not connected

nets (from the pcb view):
  N1: Part1.GND, R1.leg1, R2.leg1, R3.leg1, R4.leg1, C1.-, R7.Pin_0, R8.Pin_0, R9.Pin_0, J2.pin2
  N2: Part1.D2, R7.Pin_1, S4.Pin_1, S4.Pin_2
  N3: Part1.D3, S2.Pin_1, S2.Pin_2, R8.Pin_1
  N4: Part1.D4, S3.Pin_1, S3.Pin_2, R9.Pin_1
  N5: Part1.D5, J1.pin2
  N6: Part1.5V, S2.Pin_3, S2.Pin_4, C1.+, S3.Pin_3, S3.Pin_4, S4.Pin_3, S4.Pin_4
  N7: Part1.A3, R1.wiper
  N8: Part1.A2, R3.wiper
  N9: Part1.A1, R4.wiper
  N10: Part1.A0, R2.wiper
  N11: R1.leg2, R2.leg2, R3.leg2, R4.leg2

notes:
  1st button = Mode
  2nd button = forward
  3rd button = backward
  Leads out to LED strip
  Red = (+)
  Black = (gnd)
  Blue = Data
  *** This is not the 'ideal' method of providing power for the LED strip in this configuration. It would be best for a sepereate power supply for the LED that is sufficient for them and simply join the ground of that supply with the ground for the arduino. They can be the same supply, but power should be run to the LEDs and Arduino seperately. Adafruit sells large supplies for this purpose.
  This project is intended to be installed into a small 3D printed case with a DC jack for power and another jack to units of RGBW LEDs connected serially. That power supply should be branched off to power the arduino and LEDs seperately.
  Pots control R, G, B, and max brightness
  Red
  A3
  Grn
  A2
  Blu
  A1
  MAX
  A0
  Switches set up how many LEDs are on the connected strip(s)
  ( + )
  D2
  ( - )
  D3
  Mode
  D4
  Notice the capacitor stradling the power leads
  Pulldown resistors
  Resistor on the data line
