# Fritzing sketch id978_CableGun_0 (saved by Fritzing 0.9.3b)

parts:
  Part1 = Arduino Uno (Rev3)
  Right_Panel = 74HC595 [package="DIP16 [THT]"]
  Left_Panel = 74HC595 [package="DIP16 [THT]"]
  R1 = Resistor [tolerance=±5% resistance=470 package=THT]  # not connected
  R2 = Resistor [tolerance=±5% resistance=470 package=THT]  # not connected
  R3 = Resistor [tolerance=±5% resistance=470 package=THT]  # not connected
  R4 = Resistor [tolerance=±5% resistance=470 package=THT]  # not connected
  R5 = Resistor [tolerance=±5% resistance=470 package=THT]  # not connected
  R6 = Resistor [tolerance=±5% resistance=470 package=THT]  # not connected
  R7 = Resistor [tolerance=±5% resistance=470 package=THT]  # not connected
  LED1 = LED - 5mm [color="Red (633nm)" package="5 mm [THT]"]
  LED2 = LED - 5mm [color="Red (633nm)" package="5 mm [THT]"]
  LED3 = LED - 5mm [color="Red (633nm)" package="5 mm [THT]"]
  R9 = Resistor [tolerance=±5% resistance=470 package=THT]
  R10 = Resistor [tolerance=±5% resistance=470 package=THT]
  R11 = Resistor [tolerance=±5% resistance=470 package=THT]
  LED4 = LED - 5mm [color="Red (633nm)" package="5 mm [THT]"]
  LED5 = LED - 5mm [color="Red (633nm)" package="5 mm [THT]"]
  LED6 = LED - 5mm [color="Red (633nm)" package="5 mm [THT]"]
  LED7 = LED - 5mm [color="Orange (620nm)" package="5 mm [THT]"]
  LED8 = LED - 5mm [color="Orange (620nm)" package="5 mm [THT]"]
  LED9 = LED - 5mm [color="Orange (620nm)" package="5 mm [THT]"]
  LED10 = LED - 5mm [color="Orange (620nm)" package="5 mm [THT]"]
  LED11 = LED - 5mm [color="Yellow (595nm)" package="5 mm [THT]"]
  LED12 = LED - 5mm [color="Yellow (595nm)" package="5 mm [THT]"]
  R12 = Resistor [tolerance=±5% resistance=470 package=THT]
  R13 = Resistor [tolerance=±5% resistance=470 package=THT]
  LED13 = LED - 5mm [color="Yellow (595nm)" package="5 mm [THT]"]
  LED14 = LED - 5mm [color="Yellow (595nm)" package="5 mm [THT]"]
  R14 = Resistor [tolerance=±5% resistance=470 package=THT]
  R15 = Resistor [tolerance=±5% resistance=470 package=THT]
  LED15 = LED - 5mm [color="Blue (430nm)" package="5 mm [THT]"]
  R16 = Resistor [tolerance=±5% resistance=470 package=THT]
  LED16 = LED - 5mm [color="Blue (430nm)" package="5 mm [THT]"]
  R17 = Resistor [tolerance=±5% resistance=470 package=THT]
  VCC1 = Battery

nets:
  N1: Part1.D10_PWM/SS, R16.Pin_1
  GND: Part1.GND, Right_Panel.Q7, Right_Panel.GND, Right_Panel.OE, Left_Panel.GND, Left_Panel.OE, LED1.cathode, LED2.cathode, LED3.cathode, R9.Pin_1, R10.Pin_1, R11.Pin_0, R11.Pin_1, LED4.cathode, LED4.anode, LED5.cathode, LED5.anode, LED6.cathode, LED6.anode, LED7.cathode, LED7.anode, LED8.cathode, LED8.anode, LED9.cathode, LED10.cathode, LED11.cathode, LED12.cathode, R12.Pin_1, R13.Pin_1, LED13.cathode, LED13.anode, LED14.cathode, LED14.anode, R14.Pin_1, R15.Pin_1, LED16.anode, VCC1.+
  N2: Part1.D2, Right_Panel.ST_CP
  N3: Part1.D3_PWM, Right_Panel.DS, Right_Panel.Q0
  5V: Part1.D4, Part1.5V, Right_Panel.MR, Right_Panel.SH_CP, Right_Panel.VCC
  N4: Part1.D5_PWM, Left_Panel.ST_CP
  N5: Part1.D6_PWM, Left_Panel.DS
  N6: Part1.D7, Left_Panel.SH_CP
  3V3: Part1.3V3, Left_Panel.MR, Left_Panel.VCC
  N7: Part1.VIN, VCC1.-
  N8: LED15.anode, R17.Pin_1
