# Fritzing sketch id979_cajuzinho_0 (saved by Fritzing 0.9.0b)
circuit board: 3.89183cm x 3.41cm

parts:
  LED2 = RGB LED (com. cathode, rbg) [package="5 mm [THT]"]
  LED3 = RGB LED (com. cathode, rbg) [package="5 mm [THT]"]
  LED4 = RGB LED (com. cathode, rbg) [package="5 mm [THT]"]
  S1 = Pushbutton [package="[THT]"]
  S2 = Pushbutton [package="[THT]"]
  LED1 = RGB LED (com. cathode, rbg) [package="5 mm [THT]"]
  R1 = Resistor [tolerance=±5% resistance=330 package=THT]
  R2 = Resistor [tolerance=±5% resistance=330 package=THT]
  R3 = Resistor [tolerance=±5% resistance=330 package=THT]
  R4 = Resistor [tolerance=±5% resistance=330 package=THT]
  R5 = Resistor [tolerance=±5% resistance=330 package=THT]
  R6 = Resistor [tolerance=±5% resistance=330 package=THT]
  R7 = Resistor [tolerance=±5% resistance=330 package=THT]
  R8 = Resistor [tolerance=±5% resistance=330 package=THT]
  R9 = Resistor [tolerance=±5% resistance=330 package=THT]
  R10 = Resistor [tolerance=±5% resistance=330 package=THT]
  R11 = Resistor [tolerance=±5% resistance=330 package=THT]
  R12 = Resistor [tolerance=±5% resistance=330 package=THT]
  SG1 = Buzzer 12mm [package=buzzer-12mm-ns]
  J1 = double row male pin header, 26 pins [form="♂ (male)"]

nets:
  N1: LED2.red_anode, R6.Pin_0
  N2: LED2.common_cathode, LED3.common_cathode, LED4.common_cathode, S1.Pin_3, S1.Pin_4, S2.Pin_3, S2.Pin_4, LED1.common_cathode, SG1.2, J1.pin26
  N3: LED2.blue_anode, R5.Pin_0
  N4: LED2.green_anode, R4.Pin_0
  N5: LED3.red_anode, R8.Pin_0
  N6: LED3.blue_anode, R7.Pin_0
  N7: LED3.green_anode, R9.Pin_0
  N8: LED4.red_anode, R12.Pin_0
  N9: LED4.blue_anode, R11.Pin_0
  N10: LED4.green_anode, R10.Pin_0
  N11: S1.Pin_1, J1.pin6
  N12: S2.Pin_1, S2.Pin_2, J1.pin3
  N13: LED1.red_anode, R3.Pin_0
  N14: LED1.blue_anode, R2.Pin_0
  N15: LED1.green_anode, R1.Pin_0
  N16: R1.Pin_1, J1.pin15
  N17: R2.Pin_1, J1.pin16
  N18: R3.Pin_1, J1.pin17
  N19: R4.Pin_1, J1.pin10
  N20: R5.Pin_1, J1.pin9
  N21: R6.Pin_1, J1.pin19
  N22: R7.Pin_1, J1.pin20
  N23: R8.Pin_1, J1.pin21
  N24: R9.Pin_1, J1.pin8
  N25: R10.Pin_1, J1.pin23
  N26: R11.Pin_1, J1.pin24
  N27: R12.Pin_1, J1.pin25
  N28: SG1.1, J1.pin1

notes:
  © 2014 Luiz Kill
  Cajuzinho
  lzkill.com
