# Fritzing sketch id97_3_motor_4_LED_4_button_switch_0 (saved by Fritzing 0.8.3b)
breadboards: 2

parts:
  Part1 = Arduino Uno (Rev3)
  Part2 = EasyDriver_v44
  Part3 = EasyDriver_v44
  M2 = Stepper Motor - Bipolar
  M3 = Stepper Motor - Bipolar
  LED1 = LED - 5mm [color="Red (660nm)" package="5 mm [THT]"]
  S1 = Pushbutton [package="[THT]"]
  S2 = Pushbutton [package="[THT]"]
  S3 = Pushbutton [package="[THT]"]
  S4 = Pushbutton [package="[THT]"]
  S5 = Toggle Switch [package=THT]
  M4 = Stepper Motor - Bipolar
  Power_plug1 = Power plug
  Part4 = EasyDriver_v44
  R1 = Resistor [tolerance=±5% resistance=220 package=THT]
  LED2 = LED - 5mm [color="Yellow (595nm)" package="5 mm [THT]"]
  R2 = Resistor [tolerance=±5% resistance=220 package=THT]
  R3 = Resistor [tolerance=±5% resistance=220 package=THT]
  R4 = Resistor [tolerance=±5% resistance=220 package=THT]
  LED3 = LED - 5mm [color="Blue (470nm)" package="5 mm [THT]"]
  LED4 = LED - 5mm [color="Green (570nm)" package="5 mm [THT]"]

nets:
  N1: Part1.A2, R2.Pin_0
  N2: Part1.A3, S3.Pin_3, S3.Pin_4
  N3: Part1.A4/SDA, R3.Pin_0
  N4: Part1.A5/SCL, S2.Pin_3, S2.Pin_4
  N5: Part1.ICSP_MISO, Part1.D12/MISO, R4.Pin_0
  GND: Part1.GND, Part2.GND, Part2.SLEEP, Part3.GND, LED1.anode, S1.Pin_1, S1.Pin_2, S2.Pin_1, S2.Pin_2, S3.Pin_1, S3.Pin_2, S4.Pin_1, S4.Pin_2, Power_plug1.GND, Part4.GND, LED2.anode, LED3.anode, LED4.anode
  N6: Part1.D9_PWM, S1.Pin_3, S1.Pin_4
  N7: Part1.D10_PWM/SS, Part4.STEP
  N8: Part1.D11_PWM/MOSI, Part4.DIR
  N9: Part1.D13/SCK, R1.Pin_0
  N10: Part1.D2, Part2.STEP, Part2.MS1
  N11: Part1.D3_PWM, Part2.DIR
  N12: Part1.D4, S4.Pin_3, S4.Pin_4
  N13: Part1.D6_PWM, Part3.STEP
  N14: Part1.D7, Part3.DIR
  N15: Part2.V+, Part3.V+, S5.COM, Part4.V+
  N16: Part2.OUT2A, M4.D
  N17: Part2.OUT2B, M4.B
  N18: Part2.OUT1A, M4.C
  N19: Part2.OUT1B, M4.A
  N20: Part2.MS2, S5.L1, Power_plug1.VCC
  N21: Part3.OUT2A, M2.D
  N22: Part3.OUT2B, M2.B
  N23: Part3.OUT1A, M2.C
  N24: Part3.OUT1B, M2.A
  N25: M3.A, Part4.OUT1B
  N26: M3.C, Part4.OUT1A
  N27: M3.B, Part4.OUT2B
  N28: M3.D, Part4.OUT2A
  N29: LED1.cathode, R1.Pin_1
  N30: LED2.cathode, R2.Pin_1
  N31: R3.Pin_1, LED3.cathode
  N32: R4.Pin_1, LED4.cathode
