# Fritzing sketch id980_calandria_PCBGoodie_SL_0 (saved by Fritzing 0.9.0b)
circuit board: 4.75494cm x 3.33587cm
breadboards: 1

parts:
  jack = Audio Jack (TRS) 3.5mm [package="4Ucon 08780 [THT]"]
  R2 = Rotary Potentiometer (Large) [maximum_resistance=1mΩ package=THT]
  R1 = Rotary Potentiometer (Large) [maximum_resistance=1mΩ package=THT]
  R4 = Resistor [tolerance=±5% resistance=330 package=THT]
  LED1 = LED - 3mm [color="White (8000K)" package="3 mm [THT]"]
  D1 = Rectifier Diode [part_number=1N4001 package="300 mil [THT]"]
  C3 = Ceramic Capacitor [capacitance=100nF voltage=16V package="100 mil [THT, multilayer]"]
  22uF = Electrolytic Capacitor [capacitance=22µF package="100 mil [THT, electrolytic]"]
  40106 = IC, DIP package, 14 pins [chip_label=CD40106]
  LDR = Photocell (LDR) [package=THT]
  J1 = Piezo Speaker
  Power_plug1 = Power plug

nets:
  GND: jack.Sleeve, LED1.cathode, C3.0, 22uF.-, 40106.pin7, J1.pin1, Power_plug1.GND
  N1: jack.Ring, jack.Tip, R2.leg1, 40106.pin2, J1.pin2
  N2: R2.wiper, LDR.pin_0
  N3: R1.leg1, 22uF.+, 40106.pin13
  N4: R1.wiper, R4.Pin_1, 40106.pin12
  N5: R4.Pin_0, LED1.anode
  N6: D1.cathode, 40106.pin14
  N7: D1.anode, Power_plug1.VCC
  N8: C3.1, 40106.pin1, LDR.pin_1

notes:
  calandria
