# Fritzing sketch id981_calcul_distance_with_a_arduino_and_a_HT_SR04(ultrasonic_sensor)_0 (saved by Fritzing 0.9.1b)
breadboards: 1

parts:
  Composant1 = Arduino Uno (Rev3)
  U1 = QRD1114 [package=qrd1114]

nets:
  N1: Composant1.GND, U1.A
  N2: Composant1.D2, U1.C
  N3: Composant1.D3_PWM, U1.E
  N4: Composant1.5V, U1.K

notes:
  ceci represente un ultrasonic sensor
  ht-SR04
  le vert= echo
  le bleu= trig
  pour afficher la distance => lancer le moniteur série du programme arduino
