# Fritzing sketch id984_Devre_sema_0 (saved by Fritzing 0.9.3b)
breadboards: 1

parts:
  LCD1 = LCD screen
  Pro_Micro3 = ProMicro_01
  R1 = Rotary Potentiometer (Small) [maximum_resistance=100kΩ package=THT]
  S2 = Pushbutton [package="[THT]"]
  R2 = Rotary Potentiometer (Small) [maximum_resistance=100kΩ package=THT]
  R3 = Rotary Potentiometer (Small) [maximum_resistance=100kΩ package=THT]
  R4 = Resistor [tolerance=±5% resistance=220 package=THT]

nets:
  N1: LCD1.DB3, LCD1.DB7, LCD1.LED+, Pro_Micro3.connector23, R1.leg1, S2.Pin_3, S2.Pin_4, R2.leg1, R3.leg1, R4.Pin_0
  N2: LCD1.DB5, R1.wiper
  N3: LCD1.DB6, Pro_Micro3.connector21, R1.leg2, R2.leg2, R3.leg2
  N4: LCD1.LED-, R2.wiper
  N5: S2.Pin_1, S2.Pin_2, R4.Pin_1

notes:
  LCD giriş numaraları
  14 -13-12-11-10-9-8-7-6-5-4-3-2-1-16-15
  Anahtar 2 bacaklı, direnç önemli değil. buradaki 570ohm
  Potansiyometreler çok önemli değil
  Buradakiler aynı bile değil
  soldan sağa, B50K, B5K, B10K
