# Fritzing sketch id986_ledddi_0 (saved by Fritzing 0.8.7b)
breadboards: 1

parts:
  Parte1 = Arduino Uno (Rev3)
  R1 = Resistor [tolerance=±5% resistance=220 package=THT]
  R2 = Resistor [tolerance=±5% resistance=220 package=THT]
  LED1 = LED - 5mm [color="Red (633nm)" package="5 mm [THT]"]
  LED2 = LED - 5mm [color="Red (633nm)" package="5 mm [THT]"]

nets:
  N1: Parte1.D12/MISO, LED1.anode
  N2: Parte1.D13/SCK, LED2.anode
  N3: Parte1.GND, R1.Pin_1, R2.Pin_1
  N4: R1.Pin_0, LED1.cathode
  N5: R2.Pin_0, LED2.cathode
