# Fritzing sketch id987_led_0 (saved by Fritzing 0.8.7b)
breadboards: 1

parts:
  Parte1 = Arduino Uno (Rev3)
  LED1 = LED - 5mm [color="Red (633nm)" package="5 mm [THT]"]
  LED2 = LED - 5mm [color="Red (633nm)" package="5 mm [THT]"]
  R1 = Resistor [tolerance=±5% resistance=220 package=THT]
  R2 = Resistor [tolerance=±5% resistance=220 package=THT]

nets:
  N1: Parte1.D12/MISO, LED2.anode
  N2: Parte1.D13/SCK, LED1.anode
  N3: Parte1.GND, R1.Pin_1, R2.Pin_1
  N4: LED1.cathode, R2.Pin_0
  N5: LED2.cathode, R1.Pin_0
