# Fritzing sketch id98_Hall_Effect_Sensor_0 (saved by Fritzing 0.9.3b)
circuit board: 8.46667cm x 5.64444cm
breadboards: 1

parts:
  part = Arduino Leonardo (Rev3b)
  R1 = Resistor [tolerance=±5% resistance=220 package=THT]
  3-pins_Hall_Effect_Sensor = mystery part, 3 pins [chip_label="Hall Effect Sensor"]

nets:
  N1: part.5V, 3-pins_Hall_Effect_Sensor.pin2
  N2: part.GND, 3-pins_Hall_Effect_Sensor.pin1
  N3: part.A5, R1.Pin_0, R1.Pin_1, 3-pins_Hall_Effect_Sensor.pin3
