# Fritzing sketch id990_Camera_Timelapse_final_0 (saved by Fritzing 0.7.10b)
breadboards: 1

parts:
  Arduino1 = Arduino
  M1 = Stepper Motor - Bipolar
  R7 = Resistor [tolerance=±5% resistance=220 package=THT]
  CAM1 = Audio Jack (TRS) 3.5mm [package="4Ucon 08780 [THT]"]
  R1 = Resistor [tolerance=±5% resistance=220 package=THT]
  R2 = Resistor [tolerance=±5% resistance=220 package=THT]
  R3 = Resistor [tolerance=±5% resistance=220 package=THT]
  R4 = Resistor [tolerance=±5% resistance=220 package=THT]
  LED4 = LED - 5mm [color="Blue (505nm)" package="5 mm [THT]"]
  LED1 = LED - 5mm [color="Green (560nm)" package="5 mm [THT]"]
  LED2 = LED - 5mm [color="Yellow (585nm)" package="5 mm [THT]"]
  LED3 = LED - 5mm [color="Red (633nm)" package="5 mm [THT]"]
  R6 = Resistor [tolerance=±5% resistance=15k package=THT]
  R5 = Resistor [tolerance=±5% resistance=15k package=THT]
  U3 = TLP621 [package=THT]
  CAM2 = Audio Jack (TRS) 3.5mm [package="4Ucon 08780 [THT]"]
  CAM3 = Audio Jack (TRS) 3.5mm [package="4Ucon 08780 [THT]"]

nets:
  N1: Arduino1.GND, LED4.cathode, LED1.cathode, LED2.cathode, LED3.cathode, R6.Pin_0, R5.Pin_0, U3.Pin_2
  N2: Arduino1.D11, M1.A
  N3: Arduino1.D10, M1.C
  N4: Arduino1.D9, M1.B
  N5: Arduino1.D8, M1.D
  N6: Arduino1.D7, R1.Pin_1
  N7: Arduino1.D6, R7.Pin_0, R2.Pin_1
  N8: Arduino1.D5, R3.Pin_1
  N9: Arduino1.D4, R4.Pin_1
  N10: Arduino1.D1TX, R6.Pin_1, CAM2.Sleeve
  N11: Arduino1.D0RX, R5.Pin_1, CAM3.Sleeve
  N12: Arduino1.+5V, CAM2.Ring, CAM3.Ring
  N13: R7.Pin_1, U3.Pin_1
  N14: CAM1.Sleeve, U3.Pin_4
  N15: CAM1.Ring, U3.Pin_3
  N16: R1.Pin_0, LED1.anode
  N17: R2.Pin_0, LED2.anode
  N18: R3.Pin_0, LED3.anode
  N19: R4.Pin_0, LED4.anode

notes:
  Blue LED = On / Off
  Red LED = Pause
  Yellow LED = Shutter
  Green LED = Motor moving
  Canon Time Lapse
  Motor controller
  By Steven Vacher
