# Fritzing sketch id991_proyecto_mio_0 (saved by Fritzing 0.9.3b)
breadboards: 1

parts:
  Componente1 = Arduino Uno (Rev3)
  R1 = Resistor [tolerance=±5% resistance=220 package=THT]
  LED1 = LED - 5mm [color="Red (633nm)" package="5 mm [THT]"]
  LED2 = LED - 5mm [color="Red (633nm)" package="5 mm [THT]"]
  LED3 = LED - 5mm [color="Red (633nm)" package="5 mm [THT]"]
  LED4 = LED - 5mm [color="Red (633nm)" package="5 mm [THT]"]
  LED5 = LED - 5mm [color="Red (633nm)" package="5 mm [THT]"]
  LED6 = LED - 5mm [color="Red (633nm)" package="5 mm [THT]"]
  R7 = Resistor [tolerance=±5% resistance=220 package=THT]
  R8 = Resistor [tolerance=±5% resistance=220 package=THT]
  R9 = Resistor [tolerance=±5% resistance=220 package=THT]
  R10 = Resistor [tolerance=±5% resistance=220 package=THT]
  R11 = Resistor [tolerance=±5% resistance=220 package=THT]

nets:
  N1: Componente1.D8, LED1.anode
  N2: Componente1.GND, R1.Pin_1, R7.Pin_1, R8.Pin_1, R9.Pin_1, R10.Pin_1, R11.Pin_1
  N3: Componente1.D2, LED4.anode
  N4: Componente1.D3_PWM, LED3.anode
  N5: Componente1.D4, LED2.anode
  N6: Componente1.D5_PWM, LED6.anode
  N7: Componente1.D6_PWM, LED5.anode
  N8: R1.Pin_0, LED1.cathode
  N9: LED2.cathode, R9.Pin_0
  N10: LED3.cathode, R10.Pin_0
  N11: LED4.cathode, R11.Pin_0
  N12: LED5.cathode, R7.Pin_0
  N13: LED6.cathode, R8.Pin_0
