# Fritzing sketch id992_CamShutter_bt_0 (saved by Fritzing 0.8.3b)
breadboards: 1

parts:
  Bauteil1 = Arduino Uno (Rev3)
  U1 = TLP621 [package=THT]
  U2 = mystery part, 2 pins [chip_label=CAM]
  U3 = mystery part, 4 pins [chip_label="BT MODULE"]
  LED1 = LED - 5mm [color="Red (633nm)" package="5 mm [THT]"]
  R1 = Photocell (LDR) [package=THT]
  R2 = Resistor [tolerance=±5% resistance=2.2k package=THT]
  R4 = Resistor [tolerance=±5% resistance=220 package=THT]
  R3 = Resistor [tolerance=±5% resistance=220 package=THT]

nets:
  N1: Bauteil1.A0, R1.pin_1, R2.Pin_0
  N2: Bauteil1.ICSP_MISO, Bauteil1.D12/MISO, R3.Pin_1
  N3: Bauteil1.ICSP_MOSI, Bauteil1.D11_PWM/MOSI, R4.Pin_1
  N4: Bauteil1.GND, U1.Pin_2, U3.pin3, LED1.cathode, R2.Pin_1
  N5: Bauteil1.D0/RX, U3.pin2
  N6: Bauteil1.D1/TX, U3.pin1
  N7: Bauteil1.5V, U3.pin4, R1.pin_0
  N8: U1.Pin_1, R3.Pin_0
  N9: U1.Pin_4, U2.pin2
  N10: U1.Pin_3, U2.pin1
  N11: LED1.anode, R4.Pin_0
