# Fritzing sketch id993_capacitiveSensorShield_0 (saved by Fritzing 0.9.0b)
circuit board: 6.88566cm x 5.36311cm
breadboards: 1

parts:
  Arduino = Arduino Uno (Rev3)
  Sensoren = female pin header, 9 pins [form="♀ (female)"]
  Schirm = female pin header, 9 pins [form="♀ (female)"]
  R3 = Resistor [tolerance=±5% resistance=1M package=THT]
  R2 = Resistor [tolerance=±5% resistance=1M package=THT]
  R1 = Resistor [tolerance=±5% resistance=1M package=THT]
  R4 = Resistor [tolerance=±5% resistance=1M package=THT]
  R5 = Resistor [tolerance=±5% resistance=1M package=THT]
  R6 = Resistor [tolerance=±5% resistance=1M package=THT]
  R7 = Resistor [tolerance=±5% resistance=1M package=THT]
  R8 = Resistor [tolerance=±5% resistance=1M package=THT]
  R9 = Resistor [tolerance=±5% resistance=1M package=THT]
  C3 = Ceramic Capacitor [capacitance=100nF package="100 mil [THT, multilayer]"]
  C2 = Ceramic Capacitor [capacitance=100nF package="100 mil [THT, multilayer]"]
  C6 = Ceramic Capacitor [capacitance=100nF package="100 mil [THT, multilayer]"]
  C5 = Ceramic Capacitor [capacitance=100nF package="100 mil [THT, multilayer]"]
  C4 = Ceramic Capacitor [capacitance=100nF package="100 mil [THT, multilayer]"]
  C9 = Ceramic Capacitor [capacitance=100nF package="100 mil [THT, multilayer]"]
  C8 = Ceramic Capacitor [capacitance=100nF package="100 mil [THT, multilayer]"]
  C7 = Ceramic Capacitor [capacitance=100nF package="100 mil [THT, multilayer]"]
  C1 = Ceramic Capacitor [capacitance=100nF package="100 mil [THT, multilayer]"]

nets:
  N1: Arduino.D8, Sensoren.pin4, R4.Pin_1, C4.1
  N2: Arduino.D9_PWM, R4.Pin_0, R5.Pin_0, R6.Pin_0
  N3: Arduino.D10_PWM/SS, Sensoren.pin3, R9.Pin_1, C3.1
  N4: Arduino.D11_PWM/MOSI, Sensoren.pin2, R8.Pin_1, C2.1
  N5: Arduino.D12/MISO, Sensoren.pin1, R7.Pin_1, C1.1
  N6: Arduino.D13/SCK, R7.Pin_0, R8.Pin_0, R9.Pin_0
  N7: Arduino.GND, Schirm.pin1, Schirm.pin2, Schirm.pin3, Schirm.pin4, Schirm.pin5, Schirm.pin6, Schirm.pin7, Schirm.pin8, Schirm.pin9, C3.0, C2.0, C6.0, C5.0, C4.0, C9.0, C8.0, C7.0, C1.0
  N8: Arduino.D2, R3.Pin_0, R2.Pin_0, R1.Pin_0
  N9: Arduino.D3_PWM, Sensoren.pin9, R3.Pin_1, C9.1
  N10: Arduino.D4, Sensoren.pin8, R2.Pin_1, C8.1
  N11: Arduino.D5_PWM, Sensoren.pin7, R1.Pin_1, C7.1
  N12: Arduino.D6_PWM, Sensoren.pin6, R6.Pin_1, C6.1
  N13: Arduino.D7, Sensoren.pin5, R5.Pin_1, C5.1

notes:
  Schirm
  Sensoren
