# Fritzing sketch id994_powielacz_pojemnosci_0 (saved by Fritzing 0.9.3b)
breadboards: 1

parts:
  Q1 = NPN-Transistor [part_number=BD911 package="TO92 [THT]"]
  R1 = Resistor [tolerance=±5% resistance=1k package=THT]
  V1 = DC Power [voltage=12V]
  LOAD = Resistor [tolerance=±5% resistance=220 package=THT]
  C1 = Electrolytic Capacitor [capacitance=100µF voltage=50V package="200 mil [THT, electrolytic]"]

nets:
  N1: Q1.E, LOAD.Pin_1
  N2: Q1.B, R1.Pin_0, C1.+
  N3: Q1.C, R1.Pin_1, V1.V+
  GND: V1.V-, LOAD.Pin_0
