# Fritzing sketch id995_CapacitiveBuzzer_0 (saved by Fritzing 0.9.1b)
breadboards: 1

parts:
  Part1 = Arduino Uno (Rev3)
  R1 = Resistor [tolerance=±5% resistance=1M package="0603 [SMD]"]
  J1 = Piezo Speaker

nets:
  N1: Part1.D13/SCK, J1.pin2
  N2: Part1.GND, J1.pin1
  N3: Part1.D6_PWM, R1.Pin_1
  N4: Part1.D7, R1.Pin_0

notes:
  out to antenna
