# Fritzing sketch id996_Capacitive__touch_sensor_test_0 (saved by Fritzing 0.9.3b)

parts:
  Componente1 = Arduino Uno (Rev3)
  KY-019_5V_relay_module = keyes
  J1 = female pin header, 3 pins [form="♀ (female)"]

nets:
  N1: Componente1.D10_PWM/SS, KY-019_5V_relay_module.connector0
  N2: Componente1.D2, J1.pin1
  N3: Componente1.D3_PWM, J1.pin2
  N4: Componente1.D4, J1.pin3
  N5: Componente1.5V, KY-019_5V_relay_module.connector1
  N6: Componente1.GND, KY-019_5V_relay_module.connector2

notes:
  Capacitive touch sensor test by www.adrirobot.it
  http://www.adrirobot.it/sensori/capacitive_touch_sensor/capacitive_touch_sensor.htm
  Capacitive touch sensor
