# Fritzing sketch id997_Capacitor_tester_with_halogen_lamp_0 (saved by Fritzing 0.9.3b)
circuit board: 8.46667cm x 5.64444cm
breadboards: 1

parts:
  H1 = Camdenboss CTB0158-2 [part_number="Halogen Lamp" package=THT]
  C1 = Electrolytic Capacitor [capacitance=100µF voltage=400V package="100 mil [THT, electrolytic]"]
  D1 = Rectifier Diode [part_number=1N4007 package="300 mil [THT]"]
  R1 = Resistor [tolerance=±5% resistance=43k package=THT]
  Pad1 = Pad [width=7.902222222222222 height=9.0311111111111106 connect=center]
  Pad2 = Pad [width=7.902222222222222 height=9.0311111111111106 connect=center]

nets:
  N1: H1.pin1, R1.Pin_1, Pad1.pad
  AC 230v/Cap under test: H1.pin2, D1.anode
  N2: C1.-, Pad2.pad
  N3: C1.+, D1.cathode, R1.Pin_0

notes:
  CAP
  under
  test
  Lamp
  230v AC
  Cap under test
  Plug the AC mains for few seconds, then unplug it off. The device is ready for use.
  Place capacitor on the test leads and the bulb should blink once and stay off.
  If it does not blink, or continue to blink many times, or stay lighted on, the capacitor is bad.
