# Fritzing sketch id998_capstone_0 (saved by Fritzing 0.9.2b)
breadboards: 1

parts:
  Part1 = Arduino Mega 2560 (Rev3)
  Q1 = NPN-Transistor [package="TO92 [THT]"]
  LCD1 = LCD screen
  M1 = DC Motor
  R1 = Rotary Potentiometer (Small) [maximum_resistance=100kΩ package=THT]
  D1 = Rectifier Diode [part_number=1N4001 package="300 mil [THT]"]
  R2 = Photocell (LDR) [package=THT]
  LED1 = LED - 5mm [color="Red (633nm)" package="5 mm [THT]"]
  R4 = Rotary Potentiometer (Small) [maximum_resistance=100kΩ package=THT]
  R5 = Resistor [tolerance=±5% resistance=220 package=THT]
  R6 = Resistor [tolerance=±5% resistance=220 package=THT]
  R7 = Resistor [tolerance=±5% resistance=220 package=THT]

nets:
  N1: Part1.A0, R2.pin_1
  GND: Part1.GND, Q1.E, LCD1.VSS, LCD1.R/W, LCD1.LED-, R1.leg1, R4.leg2, R6.Pin_1
  N2: Part1.D13_PWM, LCD1.DB7
  N3: Part1.D12_PWM, LCD1.DB6
  N4: Part1.D11_PWM, LCD1.DB5
  N5: Part1.D10_PWM, LCD1.DB4
  N6: Part1.3V3, LCD1.LED+
  5V: Part1.5V, LCD1.VDD, R1.leg2, R4.leg1
  N7: Part1.D2_PWM, R7.Pin_0
  N8: Part1.D4_PWM, LCD1.RS
  N9: Part1.D6_PWM, LCD1.E
  N10: Q1.B, R7.Pin_1
  N11: Q1.C, M1.pin_2, D1.anode
  N12: LCD1.V0, R1.wiper
  N13: M1.pin_1, D1.cathode
  N14: LED1.cathode, R5.Pin_1
  N15: R4.wiper, R5.Pin_0

notes:
  ]
