# Fritzing sketch id999_Untitled_Sketch_0 (saved by Fritzing 0.9.3b)
circuit board: 2.55775cm x 3.56253cm
breadboards: 1

parts:
  Q2 = NPN-Transistor [package="TO92 [THT]"]
  R1 = Resistor [tolerance=±5% resistance=220 package=THT]
  R2 = Resistor [tolerance=±5% resistance=220 package=THT]
  LED1 = LED - 5mm [color="Red (633nm)" package="5 mm [THT]"]
  LED2 = LED - 5mm [color="Red (633nm)" package="5 mm [THT]"]
  M1 = DC Motor
  S1 = Pushbutton [package=THT]
  S2 = Pushbutton [package=THT]
  VCC1 = Battery
  Q1 = NPN-Transistor [package="TO92 [THT]"]

nets:
  N1: Q2.E, R2.Pin_0
  N2: Q2.B, S1.leg1, S2.leg0, Q1.C
  N3: Q2.C, S2.leg1, VCC1.+
  N4: R1.Pin_0, Q1.E
  N5: R1.Pin_1, LED1.anode
  N6: R2.Pin_1, LED2.anode
  N7: LED1.cathode, LED2.cathode, M1.pin_2, VCC1.-
  N8: M1.pin_1, S1.leg0, Q1.B
