# Fritzing sketch id9_prototip1_0 (saved by Fritzing 0.9.2b)
breadboards: 1

parts:
  Часть1 = Arduino Uno (Rev3)
  Q1 = Basic FET P-Channel [package="TO220 [THT]"]
  J1 = Screw terminal - 2 pins [package=THT]
  LED1 = LED - 5mm [color="Red (633nm)" package="5 mm [THT]"]
  LED2 = LED - 5mm [color="Green (565nm)" package="5 mm [THT]"]
  R1 = Resistor [tolerance=±5% resistance=220 package=THT]
  Q2 = NPN-Transistor [package="TO92 [THT]"]
  R2 = Resistor [tolerance=±5% resistance=220 package=THT]
  J2 = Screw terminal - 2 pins [package=THT]
  S1 = Pushbutton [package="[THT]"]
  R3 = Resistor [tolerance=±5% resistance=10k package=THT]
  R4 = Resistor [tolerance=±5% resistance=10k package=THT]
  J3 = Piezo Speaker

nets:
  N1: Часть1.D8, J2.pin1, R4.Pin_0
  N2: Часть1.D9_PWM, R2.Pin_0
  N3: Часть1.D2, S1.Pin_1, S1.Pin_2, R3.Pin_0
  N4: Часть1.D3_PWM, R1.Pin_0
  N5: Часть1.D5_PWM, J3.pin2
  N6: Часть1.D6_PWM, LED1.cathode, LED2.anode
  N7: Часть1.D7, Q1.gate
  N8: Часть1.5V, S1.Pin_3, S1.Pin_4
  N9: Часть1.GND, Q1.source, Q2.E, R3.Pin_1, R4.Pin_1, J3.pin1
  N10: Часть1.VIN, J1.pin1
  N11: Q1.drain, J1.pin2
  N12: LED1.anode, LED2.cathode, R1.Pin_1
  N13: Q2.B, R2.Pin_1
  N14: Q2.C, J2.pin2

notes:
  К замку
